// Logisim project ALUs.circ as structural Verilog
module ALU1 (
  input  [3:0] Ra,
  input  [3:0] Rb,
  input  CLR,
  output [3:0] Rc,
  output Carry,
  output Zero
);

  wire CLK_out;
  wire [1:0] and_1_out, register_1_q;
  wire [3:0] adder_1_out, or_1_out, register_2_q, register_3_q, xnor_1_out;

  Clock #(.highDuration(1), .lowDuration(1)) CLK (.out(CLK_out));
  assign or_1_out = Rc | Ra;  // OR_Gate or_1, 4 bits wide
  Register #(.width(2)) register_1 (.D({Zero, Carry}), .Q(register_1_q), .clk(CLK_out), .clr(CLR));  // open: en
  Register #(.width(4)) register_2 (.D(or_1_out), .Q(register_2_q), .clk(CLK_out), .clr(CLR));  // open: en
  Register #(.width(4)) register_3 (.D(Rb), .Q(register_3_q), .clk(CLK_out), .clr(CLR));  // open: en
  Adder #(.width(4)) adder_1 (
    .a(register_2_q), .b(register_3_q), .out(adder_1_out), .cin(register_1_q[0]), .cout(and_1_out[1]));
  and and_1 (and_1_out[0], xnor_1_out[0], xnor_1_out[1], xnor_1_out[2], xnor_1_out[3]);
  assign xnor_1_out = ~(register_3_q ^ register_2_q);  // XNOR_Gate xnor_1, 4 bits wide
  Register #(.width(4)) register_4 (.D(adder_1_out), .Q(Rc), .clk(CLK_out), .clr(CLR));  // open: en
  Register #(.width(2)) register_5 (.D(and_1_out), .Q({Zero, Carry}), .clk(CLK_out), .clr(CLR));  // open: en

  // Notes on the sheet:
  //   inputs
  //   operands
  //   Flags
  //   Accumulator
  //   Adder
  //   Equal
  //   Zero Flag
  //   Carry Flag
  //   outputs
  //   results
endmodule

module ALU2 (
  input  CLR,
  input  [3:0] Ra,
  input  [3:0] Rb,
  output [3:0] _C_Z,
  output [3:0] Rc
);

  wire CLK_out;
  wire [1:0] comparator_1_eq;
  wire [3:0] adder_1_out, or_1_out, register_2_q, register_3_q, register_5_q;

  Clock #(.highDuration(1), .lowDuration(1)) CLK (.out(CLK_out));
  assign or_1_out = Rc | Ra;  // OR_Gate or_1, 4 bits wide
  Register #(.width(4)) register_1 (.D(register_5_q), .Q(_C_Z), .clk(CLK_out), .clr(CLR));  // open: en
  Register #(.width(4)) register_2 (.D(or_1_out), .Q(register_2_q), .clk(CLK_out), .clr(CLR));  // open: en
  Register #(.width(4)) register_3 (.D(Rb), .Q(register_3_q), .clk(CLK_out), .clr(CLR));  // open: en
  Adder #(.width(4)) adder_1 (
    .a(register_2_q), .b(register_3_q), .out(adder_1_out), .cin(_C_Z[0]), .cout(comparator_1_eq[1]));
  Comparator #(.width(4), .mode("twosComplement")) comparator_1 (
    .a(register_3_q), .b(register_2_q), .eq(comparator_1_eq[0]));  // open: gt, lt
  Register #(.width(4)) register_4 (.D(adder_1_out), .Q(Rc), .clk(CLK_out), .clr(CLR));  // open: en
  Register #(.width(4)) register_5 (
    .D({2'b00, comparator_1_eq}), .Q(register_5_q), .clk(CLK_out), .clr(CLR));  // open: en

  // Notes on the sheet:
  //   inputs
  //   operands
  //   Flags
  //   Flags
  //   Accumulator
  //   Adder
  //   Comparator
  //   Carry Flag
  //   Zero Flag
  //   results
  //   outputs
endmodule

module ALU3 (
  input  CLR,
  input  [3:0] Ra,
  input  [3:0] Rb,
  output [3:0] N_P_C_Z,
  output [3:0] Rc
);

  wire CLK_out;
  wire [3:0] adder_1_out, comparator_1_eq, or_1_out, register_2_q, register_3_q, register_5_q;

  Clock #(.highDuration(1), .lowDuration(1)) CLK (.out(CLK_out));
  assign or_1_out = Rc | Ra;  // OR_Gate or_1, 4 bits wide
  Register #(.width(4)) register_1 (.D(register_5_q), .Q(N_P_C_Z), .clk(CLK_out), .clr(CLR));  // open: en
  Register #(.width(4)) register_2 (.D(or_1_out), .Q(register_2_q), .clk(CLK_out), .clr(CLR));  // open: en
  Register #(.width(4)) register_3 (.D(Rb), .Q(register_3_q), .clk(CLK_out), .clr(CLR));  // open: en
  Adder #(.width(4)) adder_1 (
    .a(register_2_q), .b(register_3_q), .out(adder_1_out), .cin(N_P_C_Z[0]), .cout(comparator_1_eq[1]));
  Comparator #(.width(4), .mode("twosComplement")) comparator_1 (
    .a(register_3_q), .b(register_2_q), .gt(comparator_1_eq[2]), .eq(comparator_1_eq[0]),
    .lt(comparator_1_eq[3]));
  Register #(.width(4)) register_4 (.D(adder_1_out), .Q(Rc), .clk(CLK_out), .clr(CLR));  // open: en
  Register #(.width(4)) register_5 (.D(comparator_1_eq), .Q(register_5_q), .clk(CLK_out), .clr(CLR));  // open: en

  // Notes on the sheet:
  //   inputs
  //   operands
  //   Flags
  //   Flags
  //   Accumulator
  //   Adder
  //   Comparator
  //   Carry Flag
  //   Zero Flag
  //   Positive Flag
  //   Negative Flag
  //   results
  //   outputs
endmodule

module ALU4 (
  input  [3:0] Ra,
  input  [3:0] Rb,
  input  [2:0] operation,
  output [3:0] Rc,
  output [3:0] Flags
);

  wire [0:0] adder_1_cout, subtractor_1_bout;
  wire [2:0] comparator_1_gt, comparator_2_gt;
  wire [3:0] adder_1_out, divider_1_out, divider_1_rem, multiplier_1_cout, multiplier_1_out, negator_1_out,
       subtractor_1_out;

  Adder #(.width(4)) adder_1 (.a(Ra), .b(Rb), .out(adder_1_out), .cout(adder_1_cout[0]));  // open: cin
  Subtractor #(.width(4)) subtractor_1 (
    .a(Ra), .b(Rb), .out(subtractor_1_out), .bout(subtractor_1_bout[0]));  // open: bin
  Multiplier #(.width(4)) multiplier_1 (.a(Ra), .b(Rb), .out(multiplier_1_out), .cout(multiplier_1_cout));  // open: cin
  Divider #(.width(4)) divider_1 (.a(Ra), .b(Rb), .out(divider_1_out), .rem(divider_1_rem));  // open: upper
  Negator #(.width(4)) negator_1 (.in(Ra), .out(negator_1_out));
  Comparator #(.width(4), .mode("unsigned")) comparator_1 (
    .a(Ra), .b(Rb), .gt(comparator_1_gt[0]), .eq(comparator_1_gt[1]), .lt(comparator_1_gt[2]));
  Comparator #(.width(4), .mode("unsigned")) comparator_2 (
    .a(Rb), .b(Ra), .gt(comparator_2_gt[0]), .eq(comparator_2_gt[1]), .lt(comparator_2_gt[2]));
  Multiplexer #(.select(3), .width(4)) multiplexer_1 (
    .in0(adder_1_out), .in1(subtractor_1_out), .in2(multiplier_1_out), .in3(divider_1_out),
    .in4(negator_1_out), .in5(4'b0000), .in6(4'b0000), .in7(4'b0000), .out(Rc), .sel(operation));
  Multiplexer #(.select(3), .width(4)) multiplexer_2 (
    .in0({3'b000, adder_1_cout[0]}), .in1({3'b000, subtractor_1_bout[0]}), .in2(multiplier_1_cout),
    .in3(divider_1_rem), .in4(4'b0000), .in5(4'b0000), .in6({1'b0, comparator_1_gt}),
    .in7({1'b0, comparator_2_gt}), .out(Flags), .sel(operation));

  // Notes on the sheet:
  //   000 - add
  //   001 - sub
  //   011 - div
  //   inputs
  //   Operations:
  //   010 - times
  //   101 - inverter
  //   110 - compare
  //   111 - 2's complement
  //   unsigned
  //   2's complement
  //   outputs
  //   <=>
endmodule

module ALU5 (
  input  [3:0] Ra,
  input  [3:0] Rb,
  input  [2:0] operation,
  input  CLK,
  input  CLR,
  output [3:0] Rc,
  output [3:0] Flags
);

  wire [2:0] register_1_q;
  wire [3:0] alu4_1_flags, alu4_1_rc, or_1_out, register_2_q, register_3_q;

  Register #(.width(3)) register_1 (.D(operation), .Q(register_1_q), .clk(CLK), .clr(CLR));  // open: en
  Register #(.width(4)) register_2 (.D(Rb), .Q(register_2_q), .clk(CLK), .clr(CLR));  // open: en
  assign or_1_out = Ra | alu4_1_rc;  // OR_Gate or_1, 4 bits wide
  Register #(.width(4)) register_3 (.D(or_1_out), .Q(register_3_q), .clk(CLK), .clr(CLR));  // open: en
  Register #(.width(4)) register_4 (.D(alu4_1_rc), .Q(Rc), .clk(CLK), .clr(CLR));  // open: en
  ALU4 alu4_1 (.Ra(register_3_q), .Rb(register_2_q), .operation(register_1_q), .Rc(alu4_1_rc), .Flags(alu4_1_flags));
  Register #(.width(4)) register_5 (.D(alu4_1_flags), .Q(Flags), .clk(CLK), .clr(CLR));  // open: en

  // Notes on the sheet:
  //   inputs
  //   Operations:
  //   000 - add
  //   001 - sub
  //   010 - times
  //   011 - div
  //   101 - inverter
  //   Accumulator
  //   ALU
  //   110 - compare
  //   111 - 2's complement
  //   outputs
  //   <=>
endmodule

module ALU6 (
  input  [3:0] Ra,
  input  [3:0] Rb,
  input  [2:0] operation,
  input  CLK,
  input  CLR,
  output [3:0] Rc,
  output [3:0] Flags
);

  ALU5 alu5_1 (.Ra(Ra), .Rb(Rb), .operation(operation), .CLK(CLK), .CLR(CLR), .Rc(Rc), .Flags(Flags));

  // Notes on the sheet:
  //   ALU (4bits)
  //   Operations:
  //   000 - add
  //   001 - sub
  //   010 - times
  //   011 - div
  //   101 - inverter
  //   110 - compare
  //   111 - 2's complement
  //   ALU
endmodule
