// Logisim project AU_2bit.circ as structural Verilog: 5 circuits, main circuit main
module main (
);


  // Notes on the sheet:
  //   sinais de
  //   controle
  //   R/W
  //   CLK
  //   CLR
  //   MODELO DE ULA
  //   Acumulador (A)
  //   UNIDADE
  //   ARITMÉTICA
  //   FLAGS
  //   Auxiliar (B).
  //   enderecos
  //   barramentos
  //   dados
  //   Instructions
  //   0000 -     (-A)
  //   0001 -   A + B
  //   0010 -   A  - B
  //   0011 -   A ? B
  //   0100 - 
  //   0101 - 
  //   0110 - 
  //   0111 - 
  //   A <- dado 1
  //   B <- dado 2 (opcional)
  //   select  f (A, B)
  //   A <- f (A, B)  (W)
endmodule

module AUa (
  input  [3:0] Instruction,
  input  [3:0] A____B,
  output [1:0] OUTPUT,
  output [3:0] S_P_C_Z
);

  wire adder_1_cout, comparator_1_gt, not_1_out, or_4_out, subtractor_1_bout;
  wire [1:0] adder_1_out, comparator_1_eq, negator_1_out, subtractor_1_out;
  wire [3:0] demultiplexer_1_out0, demultiplexer_1_out1, demultiplexer_1_out2, demultiplexer_1_out3,
       demultiplexer_1_out4;

  Demultiplexer #(.select(3), .width(4), .tristate("false")) demultiplexer_1 (
    .out0(demultiplexer_1_out0), .out1(demultiplexer_1_out1), .out2(demultiplexer_1_out2),
    .out3(demultiplexer_1_out3), .out4(demultiplexer_1_out4), .in(A____B), .sel(Instruction[2:0]));  // open: out5, out6, out7
  Negator #(.width(2)) negator_1 (.in(demultiplexer_1_out1[3:2]), .out(negator_1_out));
  Adder #(.width(2)) adder_1 (
    .a(demultiplexer_1_out2[1:0]), .b(demultiplexer_1_out2[3:2]), .out(adder_1_out), .cin(1'b0),
    .cout(adder_1_cout));
  Subtractor #(.width(2)) subtractor_1 (
    .a(demultiplexer_1_out3[3:2]), .b(demultiplexer_1_out3[1:0]), .out(subtractor_1_out), .bin(1'b0),
    .bout(subtractor_1_bout));
  Comparator #(.width(2), .mode("twosComplement")) comparator_1 (
    .a(demultiplexer_1_out4[1:0]), .b(demultiplexer_1_out4[3:2]), .gt(comparator_1_gt),
    .eq(comparator_1_eq[0]), .lt(comparator_1_eq[1]));
  not not_1 (not_1_out, comparator_1_eq[0]);
  or or_1 (S_P_C_Z[1], subtractor_1_bout, adder_1_cout);
  buf or_2 (S_P_C_Z[2], comparator_1_gt);  // OR_Gate
  or or_3 (S_P_C_Z[3], subtractor_1_bout, negator_1_out[1], comparator_1_eq[1]);
  Multiplexer #(.select(3), .width(2)) multiplexer_1 (
    .in0(demultiplexer_1_out0[3:2]), .in1(negator_1_out), .in2(adder_1_out), .in3(subtractor_1_out),
    .in4(comparator_1_eq), .out(OUTPUT), .sel(Instruction[2:0]));  // open: in5, in6, in7
  or or_4 (or_4_out, OUTPUT[1], OUTPUT[0]);
  nor nor_1 (S_P_C_Z[0], or_4_out, not_1_out, negator_1_out[0]);

  // Notes on the sheet:
  //   INPUT
  //   Instructions
  //   1000 -   out (A)
  //   1001 -     (-A)
  //   1010 -   A  + B
  //   1011 -   A  -  B
  //   1100 -   A ? B
  //   1101 - 
  //   1110 - 
  //   1111 - 
  //   FLAGs
endmodule

module AUb (
  input  [3:0] Instruction,
  input  [1:0] A,
  input  [1:0] B,
  output [1:0] OUTPUT,
  output [3:0] S_P_C_Z
);

  AUa aua_1 (.Instruction(Instruction), .A____B({B, A}), .OUTPUT(OUTPUT), .S_P_C_Z(S_P_C_Z));

  // Notes on the sheet:
  //   INPUTs
  //   AU
  //   FLAGs
  //   Instructions
  //   1000 -   out (A)
  //   1001 -     (-A)
  //   1010 -   A  + B
  //   1011 -   A  -  B
  //   1100 -   A ? B
  //   1101 - 
  //   1110 - 
  //   1111 - 
endmodule

module AUc (
  input  [3:0] Instruction,
  input  [1:0] A,
  input  [1:0] B,
  input  CLK,
  input  CLR,
  output [1:0] OUTPUT,
  output [3:0] S_P_C_Z
);

  wire not_1_out;
  wire [1:0] aub_1_output, register_2_q, register_3_q;
  wire [3:0] aub_1_s_p_c_z, register_1_q;

  Register #(.width(4)) register_1 (.D(Instruction), .Q(register_1_q), .clk(CLK), .clr(CLR));  // open: en
  Register #(.width(2)) register_2 (.D(A), .Q(register_2_q), .clk(CLK), .clr(CLR));  // open: en
  Register #(.width(2)) register_3 (.D(B), .Q(register_3_q), .clk(CLK), .clr(CLR));  // open: en
  not not_1 (not_1_out, CLK);
  AUb aub_1 (
    .Instruction(register_1_q), .A(register_2_q), .B(register_3_q), .OUTPUT(aub_1_output),
    .S_P_C_Z(aub_1_s_p_c_z));
  Register #(.width(2)) register_4 (.D(aub_1_output), .Q(OUTPUT), .clk(not_1_out), .clr(CLR));  // open: en
  Register #(.width(4)) register_5 (.D(aub_1_s_p_c_z), .Q(S_P_C_Z), .clk(not_1_out), .clr(CLR));  // open: en

  // Notes on the sheet:
  //   INPUTs
  //   A_in
  //   A_out
  //   AU
  //   FLAGs
  //   Instructions
  //   1000 -   out (A)
  //   1001 -     (-A)
  //   1010 -   A  + B
  //   1011 -   A  -  B
  //   1100 -   A ? B
  //   1101 - 
  //   1110 - 
  //   1111 - 
endmodule

module AUd (
  input  [3:0] Instruction,
  input  R_W,
  input  [1:0] A,
  input  [1:0] B,
  input  CLK,
  input  CLR,
  output [2:0] OUTPUT,
  output [3:0] S_P_C_Z
);

  wire or_1_out;
  wire [1:0] multiplexer_1_out, register_2_q, register_3_q;
  wire [3:0] register_1_q;

  Multiplexer #(.select(1), .width(2)) multiplexer_1 (.in0(A), .in1(OUTPUT[1:0]), .out(multiplexer_1_out), .sel(R_W));
  Register #(.width(4)) register_1 (.D(Instruction), .Q(register_1_q), .clk(CLK), .clr(or_1_out));  // open: en
  or or_1 (or_1_out, R_W, CLR);
  Register #(.width(2)) register_2 (.D(multiplexer_1_out), .Q(register_2_q), .clk(CLK), .clr(CLR));  // open: en
  Register #(.width(2)) register_3 (.D(B), .Q(register_3_q), .clk(CLK), .clr(CLR));  // open: en
  AUc auc_1 (
    .Instruction(register_1_q), .A(register_2_q), .B(register_3_q), .CLK(CLK), .CLR(CLR),
    .OUTPUT(OUTPUT[1:0]), .S_P_C_Z({S_P_C_Z[3:2], OUTPUT[2], S_P_C_Z[0]}));

  assign S_P_C_Z[1] = OUTPUT[2];

  // Notes on the sheet:
  //   INPUTs
  //   Accumulator
  //   AU
  //   FLAGs
  //   Instructions
  //   1000 -   out (A)
  //   1001 -     (-A)
  //   1010 -   A  + B
  //   1011 -   A  -  B
  //   1100 -   A  ?  B
  //   1101 - 
  //   1110 - 
  //   1111 - 
endmodule
