// Logisim project LU_1bit.circ as structural Verilog: 5 circuits, main circuit main
module main (
);


  // Notes on the sheet:
  //   sinais de
  //   controle
  //   R/W
  //   CLK
  //   CLR
  //   MODELO DE ULA
  //   Acumulador (A)
  //   UNIDADE
  //   LÓGICA
  //   Auxiliar (B).
  //   enderecos
  //   barramentos
  //   dados
  //   Instrucoes
  //   0000 - out (A)
  //   0001 - not (A)
  //   0010 - and (A, B)
  //   0011 - or (A, B)
  //   0100 - nand (A, B)
  //   0101 - nor (A, B)
  //   0110 - xor (A, B)
  //   0111 - xnor (A, B)
  //   A <- dado 1
  //   B <- dado 2 (opcional)
  //   select  f (A, B)
  //   A <- f (A, B)  (W)
endmodule

module LUa (
  input  [3:0] Instruction,
  input  [1:0] INPUT,
  output OUTPUT
);

  wire and_1_out, nand_1_out, nor_1_out, not_1_out, or_1_out, xnor_1_out, xor_1_out;
  wire [1:0] demultiplexer_1_out0, demultiplexer_1_out1, demultiplexer_1_out2, demultiplexer_1_out3,
       demultiplexer_1_out4, demultiplexer_1_out5, demultiplexer_1_out6, demultiplexer_1_out7;

  Demultiplexer #(.select(3), .width(2), .tristate("false")) demultiplexer_1 (
    .out0(demultiplexer_1_out0), .out1(demultiplexer_1_out1), .out2(demultiplexer_1_out2),
    .out3(demultiplexer_1_out3), .out4(demultiplexer_1_out4), .out5(demultiplexer_1_out5),
    .out6(demultiplexer_1_out6), .out7(demultiplexer_1_out7), .in(INPUT), .sel(Instruction[2:0]));
  not not_1 (not_1_out, demultiplexer_1_out1[0]);
  and and_1 (and_1_out, demultiplexer_1_out2[0], demultiplexer_1_out2[1]);
  or or_1 (or_1_out, demultiplexer_1_out3[0], demultiplexer_1_out3[1]);
  nand nand_1 (nand_1_out, demultiplexer_1_out4[0], demultiplexer_1_out4[1]);
  nor nor_1 (nor_1_out, demultiplexer_1_out5[0], demultiplexer_1_out5[1]);
  xor xor_1 (xor_1_out, demultiplexer_1_out6[0], demultiplexer_1_out6[1]);
  xnor xnor_1 (xnor_1_out, demultiplexer_1_out7[0], demultiplexer_1_out7[1]);
  Multiplexer #(.select(3), .width(1)) multiplexer_1 (
    .in0(demultiplexer_1_out0[0]), .in1(not_1_out), .in2(and_1_out), .in3(or_1_out), .in4(nand_1_out),
    .in5(nor_1_out), .in6(xor_1_out), .in7(xnor_1_out), .out(OUTPUT), .sel(Instruction[2:0]));
endmodule

module LUb (
  input  [3:0] Instruction,
  input  A,
  input  B,
  output OUTPUT
);

  LUa lua_1 (.Instruction(Instruction), .INPUT({B, A}), .OUTPUT(OUTPUT));

  // Notes on the sheet:
  //   INPUTs
  //   LU
  //   0000 - out (A)
  //   0001 - not (A)
  //   0011 - or (A, B)
  //   Instructions
  //   0010 - and (A, B)
  //   0100 - nand (A, B)
  //   0101 - nor (A, B)
  //   0110 - xor (A, B)
  //   0111 - xnor (A, B)
endmodule

module LUc (
  input  [3:0] Instruction,
  input  A,
  input  B,
  input  CLK,
  input  CLR,
  output OUTPUT
);

  wire lua_1_output, not_1_out;
  wire [1:0] d_ff_1_q;
  wire [3:0] register_1_q;

  Register #(.width(4)) register_1 (.D(Instruction), .Q(register_1_q), .clk(CLK), .clr(CLR));  // open: en
  D_Flip_Flop d_ff_1 (.clk(CLK), .D(A), .Q(d_ff_1_q[0]), .reset(CLR));  // open: Qn, preset, en
  D_Flip_Flop d_ff_2 (.clk(CLK), .D(B), .Q(d_ff_1_q[1]), .reset(CLR));  // open: Qn, preset, en
  not not_1 (not_1_out, CLK);
  LUa lua_1 (.Instruction(register_1_q), .INPUT(d_ff_1_q), .OUTPUT(lua_1_output));
  D_Flip_Flop d_ff_3 (.clk(not_1_out), .D(lua_1_output), .Q(OUTPUT), .reset(CLR));  // open: Qn, preset, en

  // Notes on the sheet:
  //   INPUTs
  //   A_in
  //   LU
  //   A_out
  //   Instructions
  //   0000 - out (A)
  //   0001 - not (A)
  //   0010 - and (A, B)
  //   0011 - or (A, B)
  //   0100 - nand (A, B)
  //   0101 - nor (A, B)
  //   0110 - xor (A, B)
  //   0111 - xnor (A, B)
endmodule

module LUd (
  input  [3:0] Instruction,
  input  R_W,
  input  A,
  input  B,
  input  CLK,
  input  CLR,
  output OUTPUT
);

  wire and_1_out, or_1_out;
  wire [1:0] d_ff_1_q;
  wire [3:0] register_1_q;

  and and_1 (and_1_out, R_W, OUTPUT);
  or or_1 (or_1_out, and_1_out, A);
  Register #(.width(4)) register_1 (.D(Instruction), .Q(register_1_q), .clk(CLK), .clr(CLR));  // open: en
  D_Flip_Flop d_ff_1 (.clk(CLK), .D(or_1_out), .Q(d_ff_1_q[0]), .reset(CLR));  // open: Qn, preset, en
  D_Flip_Flop d_ff_2 (.clk(CLK), .D(B), .Q(d_ff_1_q[1]), .reset(CLR));  // open: Qn, preset, en
  LUa lua_1 (.Instruction(register_1_q), .INPUT(d_ff_1_q), .OUTPUT(OUTPUT));

  // Notes on the sheet:
  //   INPUTs
  //   Accumulator
  //   LU
  //   Instructions
  //   0000 - out (A)
  //   0001 - not (A)
  //   0010 - and (A, B)
  //   0011 - or (A, B)
  //   0100 - nand (A, B)
  //   0101 - nor (A, B)
  //   0110 - xor (A, B)
  //   0111 - xnor (A, B)
endmodule
