// Logisim project UC.circ as structural Verilog: 4 circuits, main circuit main
module main (
);


  // Notes on the sheet:
  //   sinais de
  //   controle
  //   R/W
  //   CLK
  //   CLR
  //   MODELO DE UC
  //   Contador de
  //   programa (PC)
  //   DECODIFICADOR
  //   E
  //   SEQUENCIADOR
  //   Registrador de
  //   instrucao (RI)
  //   enderecos
  //   barramentos
  //   dados
  //   Instructions
  //   0000 -     (-A)
  //   0001 -   A + B
  //   0010 -   A  - B
  //   0011 -   A ? B
  //   0100 - 
  //   0101 - 
  //   0110 - 
  //   0111 - 
  //   Ciclo de busca de instrucao:
  //   PC <- endereco atual
  //   RI  <- copia da instrucao
  //    decodificar instrucao
  //   PC <- proximo endereco
endmodule

module PC (
  input  CLK,
  input  RESET,
  output [5:0] PC
);

  wire [5:0] register_1_q;

  Register #(.width(6)) register_1 (.D(PC), .Q(register_1_q), .clk(CLK), .clr(RESET));  // open: en
  Adder #(.width(6)) adder_1 (.a(register_1_q), .b(6'b000001), .out(PC), .cin(1'b0));  // open: cout

  // Notes on the sheet:
  //   Program Counter (6bits)
  //   adder
endmodule

module Decoder (
  input  [10:0] in_1,
  output A,
  output B,
  output C,
  output D,
  output [1:0] op_1__X,
  output [1:0] op_2__Y,
  output [3:0] RI,
  output data
);

  Decoder_part #(.select(2), .tristate("false")) decoder_1 (.out0(A), .out1(B), .out2(C), .out3(D), .sel(in_1[10:9]));

  assign data = in_1[0];
  assign op_1__X = in_1[8:7];
  assign op_2__Y = in_1[6:5];
  assign RI = in_1[4:1];

  // Notes on the sheet:
  //   Decoder
  //   Instruction
  //   Registers
  //   result
endmodule

module UC (
  input  CLK,
  input  RESET,
  output [1:0] result,
  output [1:0] op_1,
  output [1:0] op_2,
  output [3:0] operation,
  output data,
  output [5:0] REM,
  output [10:0] RDM
);

  wire decoder_1_b, decoder_1_data;

  PC pc_1 (.CLK(CLK), .RESET(RESET), .PC(REM));
  Decoder decoder_1 (
    .in_1(RDM), .A(data), .op_1__X(op_1), .op_2__Y(op_2), .RI(operation), .data(decoder_1_data),
    .B(decoder_1_b), .C(result[1]), .D(result[0]));
  ROM #(.addrWidth(6), .dataWidth(11)) rom_1 (.addr(REM), .data(RDM));  // open: sel

  // Notes on the sheet:
  //   Control Unit
  //   decoder
  //   PC
  //   contents of rom_1 (hex, n*v repeats v):
  //   0 1 2 3 4 5 6 7 8 9 a b c d e f 10 11 12 13 14 15 16 17 18 19 1a 1b 1c 1d 1e 1f
  //   ROM
endmodule
