// Logisim project CPU.circ as structural Verilog: 7 circuits, main circuit main
module main (
);


  // Notes on the sheet:
  //   CPU 1bit
  //   Registradores
  //   A - 00
  //   B - 01
  //   C - 10
  //   D - 11
  //   ISL 2006/2
  //   Operações
  //   xor - 0000
  //   and - 0001
  //   or - 0010
  //   nand - 0011
  //   not 0100
  //   nor - 0101
  //   add - 0110
  //   x -1101
  //   y - 1100
  //   load - 1111
  //   Unidade de controle
  //   Decoder
  //   RI
  //   PC
  //   Clock
  //   REM
  //   Arquitetura de Computador
  //   Interfaces (I/O)
  //   Memória
  //   RDM
  //   Unidade
  //   Lógica
  //   e
  //   Aritmética
  //   barramento de
  //   dados e endereços
  //   PUC-Minas
endmodule

module PC (
  input  CLK,
  input  RESET,
  output [5:0] PC
);

  wire [5:0] register_1_q;

  Register_part #(.width(6)) register_1 (.D(PC), .Q(register_1_q), .clk(CLK), .clr(RESET));  // open: en
  Adder #(.width(6)) adder_1 (.a(register_1_q), .b(6'b000001), .out(PC));  // open: cin, cout

  // Notes on the sheet:
  //   Program Counter (6bits)
  //   adder
endmodule

module ROM (
  input  CLK,
  input  RESET,
  output [5:0] REM,
  output [5:0] RDM
);

  PC pc_1 (.CLK(CLK), .RESET(RESET), .PC(REM));
  ROM_part #(.addrWidth(6), .dataWidth(6)) rom_1 (.addr(REM), .data(RDM));  // open: sel

  // Notes on the sheet:
  //   Memory (ROM)
  //   PC
endmodule

module Decoder (
  input  CLK,
  input  RESET,
  output A,
  output B,
  output C,
  output D,
  output [1:0] op_1,
  output [1:0] op_2,
  output [3:0] RI,
  output data,
  output [5:0] REM,
  output [10:0] RDM
);

  Decoder_part #(.select(2), .tristate("false")) decoder_1 (.out0(A), .out1(B), .out2(C), .out3(D), .sel(RDM[10:9]));
  PC pc_1 (.CLK(CLK), .RESET(RESET), .PC(REM));
  ROM_part #(.addrWidth(6), .dataWidth(11)) rom_1 (
    .addr(REM), .data({RDM[10:9], op_1, op_2, RDM[4:1], data}));  // open: sel

  assign {RDM[8:5], RDM[0]} = {op_1, op_2, data};
  assign RI = RDM[4:1];

  // Notes on the sheet:
  //   Decoder
  //   PC
  //   contents of rom_1 (hex, n*v repeats v):
  //   0 1 10 11 100 101 110 111
endmodule

module ALU (
  input  RESET,
  input  CLK,
  output [3:0] ABCD,
  output FLAGS,
  output A,
  output B,
  output C,
  output D,
  output [1:0] op_1,
  output [1:0] op_2,
  output [3:0] RI,
  output data,
  output [5:0] REM,
  output [10:0] RDM
);

  wire adder_1_out, and_1_out, multiplexer_1_out, multiplexer_2_out, multiplexer_3_out, nand_1_out,
       nor_1_out, not_1_out, or_1_out, xor_1_out;

  Decoder_part #(.select(2), .tristate("false")) decoder_1 (
    .out0(ABCD[3]), .out1(ABCD[2]), .out2(ABCD[1]), .out3(ABCD[0]), .sel(RDM[10:9]));
  PC pc_1 (.CLK(CLK), .RESET(RESET), .PC(REM));
  ROM_part #(.addrWidth(6), .dataWidth(11)) rom_1 (
    .addr(REM), .data({RDM[10:9], op_1, op_2, RDM[4:1], data}));  // open: sel
  Register register_1 (.data(multiplexer_3_out), .enable(ABCD[3]), .A(A));  // open: A_2
  Register register_2 (.data(multiplexer_3_out), .enable(ABCD[2]), .A(B));  // open: A_2
  Register register_3 (.data(multiplexer_3_out), .enable(ABCD[1]), .A(C));  // open: A_2
  Register register_4 (.data(multiplexer_3_out), .enable(ABCD[0]), .A(D));  // open: A_2
  Multiplexer #(.select(2), .width(1)) multiplexer_1 (
    .in0(A), .in1(B), .in2(C), .in3(D), .out(multiplexer_1_out), .sel(op_1));
  Multiplexer #(.select(2), .width(1)) multiplexer_2 (
    .in0(A), .in1(B), .in2(C), .in3(D), .out(multiplexer_2_out), .sel(op_2));
  xor xor_1 (xor_1_out, multiplexer_1_out, multiplexer_2_out);
  and and_1 (and_1_out, multiplexer_1_out, multiplexer_2_out);
  or or_1 (or_1_out, multiplexer_1_out, multiplexer_2_out);
  nand nand_1 (nand_1_out, multiplexer_1_out, multiplexer_2_out);
  not not_1 (not_1_out, multiplexer_2_out);
  nor nor_1 (nor_1_out, multiplexer_1_out, multiplexer_2_out);
  Adder #(.width(1)) adder_1 (
    .a(multiplexer_1_out), .b(multiplexer_2_out), .out(adder_1_out), .cout(FLAGS));  // open: cin
  Multiplexer #(.select(4), .width(1)) multiplexer_3 (
    .in0(xor_1_out), .in1(and_1_out), .in2(or_1_out), .in3(nand_1_out), .in4(not_1_out), .in5(nor_1_out),
    .in6(adder_1_out), .in7(1'b0), .in8(1'b0), .in9(1'b0), .in10(1'b0), .in11(1'b0), .in12(1'b0),
    .in13(multiplexer_1_out), .in14(multiplexer_2_out), .in15(data), .out(multiplexer_3_out), .sel(RDM[4:1]));

  assign {RDM[8:5], RDM[0]} = {op_1, op_2, data};
  assign RI = RDM[4:1];

  // Notes on the sheet:
  //   ALU
  //   PC
  //   contents of rom_1 (hex, n*v repeats v):
  //   0 0 1f 1e 21f 21e 41f 41e 61f 61e 0 21f 620 424 266 48 21f 41f cc
  //   A
  //   B
  //   C
  //   D
endmodule

module RAM (
  input  [1:0] address,
  input  CLK,
  input  R_W,
  input  data_in,
  input  CLR,
  output data_out
);

  wire and_1_out, and_2_out, and_3_out, and_4_out, and_5_out, and_6_out, and_7_out, and_8_out, d_ff_1_q,
       d_ff_2_q, d_ff_3_q, d_ff_4_q, decoder_1_out0, decoder_1_out1, decoder_1_out2, decoder_1_out3,
       not_1_out;

  Decoder_part #(.select(2), .tristate("false")) decoder_1 (
    .out0(decoder_1_out0), .out1(decoder_1_out1), .out2(decoder_1_out2), .out3(decoder_1_out3), .sel(address));
  and and_1 (and_1_out, data_in, R_W, decoder_1_out3);
  not not_1 (not_1_out, R_W);
  D_Flip_Flop d_ff_1 (.clk(CLK), .Q(d_ff_1_q), .preset(and_1_out), .reset(CLR));  // open: D, Qn, en
  and and_2 (and_2_out, data_in, R_W, decoder_1_out2);
  and and_3 (and_3_out, decoder_1_out3, not_1_out, d_ff_1_q);
  D_Flip_Flop d_ff_2 (.clk(CLK), .Q(d_ff_2_q), .preset(and_2_out), .reset(CLR));  // open: D, Qn, en
  and and_4 (and_4_out, data_in, R_W, decoder_1_out1);
  and and_5 (and_5_out, decoder_1_out2, not_1_out, d_ff_2_q);
  Multiplexer #(.select(2), .width(1)) multiplexer_1 (
    .in0(and_8_out), .in1(and_7_out), .in2(and_5_out), .in3(and_3_out), .out(data_out), .sel(address));
  D_Flip_Flop d_ff_3 (.clk(CLK), .Q(d_ff_3_q), .preset(and_4_out), .reset(CLR));  // open: D, Qn, en
  and and_6 (and_6_out, data_in, R_W, decoder_1_out0);
  and and_7 (and_7_out, decoder_1_out1, not_1_out, d_ff_3_q);
  D_Flip_Flop d_ff_4 (.clk(CLK), .Q(d_ff_4_q), .preset(and_6_out), .reset(CLR));  // open: D, Qn, en
  and and_8 (and_8_out, decoder_1_out0, not_1_out, d_ff_4_q);

  // Notes on the sheet:
  //   Memory 4x1 (RAM)
endmodule

module Register (
  input  data,
  input  enable,
  output A,
  output A_2
);

  wire and_1_out, nand_1_out, nand_2_out;

  and and_1 (and_1_out, data, enable);
  not nand_1 (nand_1_out, and_1_out);  // NAND_Gate
  nand nand_2 (nand_2_out, nand_1_out, enable);
  nand nand_3 (A, nand_1_out, A_2);
  nand nand_4 (A_2, A, nand_2_out);

  // Notes on the sheet:
  //   Register (enabled D_Latch)
endmodule
