// Logisim project MEM4x4a.circ as structural Verilog: 8 circuits, main circuit main
module main (
);


  // Notes on the sheet:
  //   sinais de
  //   controle
  //   R/W
  //   CLK
  //   CLR
  //   MODELO DE MEMÓRIA
  //   MEMÓRIA
  //   (armazenamento)
  //   endereços
  //   M.A.R.
  //   M.D.R.
  //   barramentos
  //   dados
  //   escrita
  //   leitura
  //   (endereço<-dado)
  //   (endereço->dado)
endmodule

module MemCell (
  input  Addr,
  input  R_W,
  input  D,
  input  CLR,
  output OUT
);

  wire and_1_out, and_2_out, not_1_out, s_r_ff_1_q;

  not not_1 (not_1_out, D);
  and and_1 (and_1_out, Addr, D);
  S_R_Flip_Flop s_r_ff_1 (
    .S(and_1_out), .clk(R_W), .R(and_2_out), .Q(s_r_ff_1_q), .reset(CLR));  // open: Qn, preset, en
  and and_2 (and_2_out, Addr, not_1_out);
  and and_3 (OUT, Addr, s_r_ff_1_q);
endmodule

module Mem1x4a (
  input  Addr,
  input  R_W,
  input  D3,
  input  D2,
  input  D1,
  input  D0,
  input  CLR,
  output Q3,
  output Q2,
  output Q1,
  output Q0
);

  MemCell memcell_1 (.Addr(Addr), .R_W(R_W), .D(D3), .CLR(CLR), .OUT(Q3));
  MemCell memcell_2 (.Addr(Addr), .R_W(R_W), .D(D2), .CLR(CLR), .OUT(Q2));
  MemCell memcell_3 (.Addr(Addr), .R_W(R_W), .D(D1), .CLR(CLR), .OUT(Q1));
  MemCell memcell_4 (.Addr(Addr), .R_W(R_W), .D(D0), .CLR(CLR), .OUT(Q0));
endmodule

module Mem1x4b (
  input  Addr,
  input  R_W,
  input  [3:0] IN,
  input  CLR,
  output [3:0] OUT
);

  MemCell memcell_1 (.Addr(Addr), .R_W(R_W), .D(IN[3]), .CLR(CLR), .OUT(OUT[3]));
  MemCell memcell_2 (.Addr(Addr), .R_W(R_W), .D(IN[2]), .CLR(CLR), .OUT(OUT[2]));
  MemCell memcell_3 (.Addr(Addr), .R_W(R_W), .D(IN[1]), .CLR(CLR), .OUT(OUT[1]));
  MemCell memcell_4 (.Addr(Addr), .R_W(R_W), .D(IN[0]), .CLR(CLR), .OUT(OUT[0]));
endmodule

module Mem4x4a (
  input  [1:0] Addr,
  input  R_W,
  input  [3:0] IN,
  input  CLR,
  output [3:0] OUT
);

  wire decoder_1_out0, decoder_1_out1, decoder_1_out2, decoder_1_out3;
  wire [3:0] demultiplexer_1_out0, demultiplexer_1_out1, demultiplexer_1_out2, demultiplexer_1_out3,
       mem1x4b_1_out, mem1x4b_2_out, mem1x4b_3_out, mem1x4b_4_out;

  Decoder #(.select(2), .tristate("false")) decoder_1 (
    .out0(decoder_1_out0), .out1(decoder_1_out1), .out2(decoder_1_out2), .out3(decoder_1_out3), .sel(Addr));
  Demultiplexer #(.select(2), .width(4), .tristate("false")) demultiplexer_1 (
    .out0(demultiplexer_1_out0), .out1(demultiplexer_1_out1), .out2(demultiplexer_1_out2),
    .out3(demultiplexer_1_out3), .in(IN), .sel(Addr));
  Mem1x4b mem1x4b_1 (.Addr(decoder_1_out3), .R_W(R_W), .IN(demultiplexer_1_out3), .CLR(CLR), .OUT(mem1x4b_1_out));
  Mem1x4b mem1x4b_2 (.Addr(decoder_1_out2), .R_W(R_W), .IN(demultiplexer_1_out2), .CLR(CLR), .OUT(mem1x4b_2_out));
  Mem1x4b mem1x4b_3 (.Addr(decoder_1_out1), .R_W(R_W), .IN(demultiplexer_1_out1), .CLR(CLR), .OUT(mem1x4b_3_out));
  Mem1x4b mem1x4b_4 (.Addr(decoder_1_out0), .R_W(R_W), .IN(demultiplexer_1_out0), .CLR(CLR), .OUT(mem1x4b_4_out));
  Multiplexer #(.select(2), .width(4)) multiplexer_1 (
    .in0(mem1x4b_4_out), .in1(mem1x4b_3_out), .in2(mem1x4b_2_out), .in3(mem1x4b_1_out), .out(OUT), .sel(Addr));
endmodule

module Mem4x4b (
  input  [1:0] MAR,
  input  R_W,
  input  [3:0] MDRin,
  input  CLR,
  output [3:0] MDRout
);

  Mem4x4a mem4x4a_1 (.Addr(MAR), .R_W(R_W), .IN(MDRin), .CLR(CLR), .OUT(MDRout));
endmodule

module Mem4x4c (
  input  [1:0] MAR,
  input  R_W,
  input  [3:0] MDRin,
  input  CLK,
  input  CLR,
  output [3:0] MDRout
);

  wire [3:0] multiplexer_1_out;

  Mem4x4a mem4x4a_1 (.Addr(MAR), .R_W(CLK), .IN(multiplexer_1_out), .CLR(CLR), .OUT(MDRout));
  Multiplexer #(.select(1), .width(4)) multiplexer_1 (.in0(MDRout), .in1(MDRin), .out(multiplexer_1_out), .sel(R_W));
endmodule

module Mem4x4d (
  input  [1:0] address,
  input  read_write,
  input  [3:0] \input ,
  input  clock,
  input  clear,
  output [3:0] \output 
);

  wire not_1_out;
  wire [1:0] register_1_q;
  wire [3:0] mem4x4c_1_mdrout, register_2_q;

  Register #(.width(2)) register_1 (.D(address), .Q(register_1_q), .clk(clock), .clr(clear));  // open: en
  Register #(.width(4)) register_2 (.D(\input ), .Q(register_2_q), .clk(clock), .clr(clear));  // open: en
  Mem4x4c mem4x4c_1 (
    .MAR(register_1_q), .R_W(read_write), .MDRin(register_2_q), .CLK(clock), .CLR(clear),
    .MDRout(mem4x4c_1_mdrout));
  Register #(.width(4)) register_3 (.D(mem4x4c_1_mdrout), .Q(\output ), .clk(not_1_out), .clr(clear));  // open: en
  not not_1 (not_1_out, clock);

  // Notes on the sheet:
  //   MAR
  //   MDRin
  //   MEMORY
  //   4x4
  //   MDRout
endmodule
