// Logisim project RAM1x4.circ as structural Verilog: 1 circuit, main circuit main
module main (
  input  R_W,
  input  CLR,
  input  [3:0] data_in,
  output [3:0] data_out
);

  D_Flip_Flop d_ff_1 (.clk(R_W), .D(data_in[3]), .Q(data_out[3]), .reset(CLR));  // open: Qn, preset, en
  D_Flip_Flop d_ff_2 (.clk(R_W), .D(data_in[2]), .Q(data_out[2]), .reset(CLR));  // open: Qn, preset, en
  D_Flip_Flop d_ff_3 (.clk(R_W), .D(data_in[1]), .Q(data_out[1]), .reset(CLR));  // open: Qn, preset, en
  D_Flip_Flop d_ff_4 (.clk(R_W), .D(data_in[0]), .Q(data_out[0]), .reset(CLR));  // open: Qn, preset, en

  // Notes on the sheet:
  //   RAM 1x4
endmodule
