// Logisim project RAM4x4.circ as structural Verilog: 2 circuits, main circuit main
module main (
  input  R_W,
  input  [3:0] data_in,
  input  [1:0] address,
  input  CLR,
  output [3:0] data_out
);

  wire and_1_out, and_2_out, and_3_out, and_4_out, decoder_1_out0, decoder_1_out1, decoder_1_out2,
       decoder_1_out3;
  wire [3:0] ram1x4_1_data_out, ram1x4_2_data_out, ram1x4_3_data_out, ram1x4_4_data_out;

  Decoder #(.select(2), .tristate("false")) decoder_1 (
    .out0(decoder_1_out0), .out1(decoder_1_out1), .out2(decoder_1_out2), .out3(decoder_1_out3), .sel(address));
  and and_1 (and_1_out, R_W, decoder_1_out0);
  and and_2 (and_2_out, R_W, decoder_1_out1);
  and and_3 (and_3_out, R_W, decoder_1_out2);
  and and_4 (and_4_out, R_W, decoder_1_out3);
  RAM1x4 ram1x4_1 (.R_W(and_1_out), .data_in(data_in), .CLR(CLR), .data_out(ram1x4_1_data_out));
  RAM1x4 ram1x4_2 (.R_W(and_2_out), .data_in(data_in), .CLR(CLR), .data_out(ram1x4_2_data_out));
  RAM1x4 ram1x4_3 (.R_W(and_3_out), .data_in(data_in), .CLR(CLR), .data_out(ram1x4_3_data_out));
  RAM1x4 ram1x4_4 (.R_W(and_4_out), .data_in(data_in), .CLR(CLR), .data_out(ram1x4_4_data_out));
  BitSelector #(.width(16), .group(4)) bitselector_1 (
    .in({ram1x4_4_data_out, ram1x4_3_data_out, ram1x4_2_data_out, ram1x4_1_data_out}), .out(data_out),
    .sel(address));

  // Notes on the sheet:
  //   RAM 4x4
endmodule

module RAM1x4 (
  input  R_W,
  input  [3:0] data_in,
  input  CLR,
  output [3:0] data_out
);

  D_Flip_Flop d_ff_1 (.clk(R_W), .D(data_in[1]), .Q(data_out[1]), .reset(CLR));  // open: Qn, preset, en
  D_Flip_Flop d_ff_2 (.clk(R_W), .D(data_in[0]), .Q(data_out[0]), .reset(CLR));  // open: Qn, preset, en
  D_Flip_Flop d_ff_3 (.clk(R_W), .D(data_in[2]), .Q(data_out[2]), .reset(CLR));  // open: Qn, preset, en
  D_Flip_Flop d_ff_4 (.clk(R_W), .D(data_in[3]), .Q(data_out[3]), .reset(CLR));  // open: Qn, preset, en

  // Notes on the sheet:
  //   RAM 1x4
endmodule
