// Logisim project shift_adder.circ as structural Verilog: 3 circuits, main circuit main
module main (
  input  load,
  input  [2:0] data_A,
  input  [2:0] data_B,
  input  CLR,
  output Carry_flag,
  output [2:0] \output ,
  output [2:0] Ra,
  output out_8,
  output out_9,
  output [2:0] Rb
);

  wire adder_1_cout, adder_1_out, and_1_out, CLK_out, d_ff_2_q, not_1_out;
  wire [2:0] shl_1_out_7;

  Clock #(.highDuration(1), .lowDuration(1)) CLK (.out(CLK_out));
  SHR shr_1 (.in_1(load), .in_2(data_A), .in_3(CLK_out), .in_4(1'b0), .in_5(CLR), .out_6(out_8), .out_7(Ra));
  not not_1 (not_1_out, CLK_out);
  SHR shr_2 (.in_1(load), .in_2(data_B), .in_3(CLK_out), .in_4(1'b0), .in_5(CLR), .out_6(out_9), .out_7(Rb));
  D_Flip_Flop #(.trigger("rising")) d_ff_1 (
    .clk(CLK_out), .D(adder_1_cout), .Q(Carry_flag), .reset(CLR));  // open: Qn, preset, en
  Adder #(.width(1)) adder_1 (.a(out_8), .b(out_9), .out(adder_1_out), .cin(Carry_flag), .cout(adder_1_cout));
  D_Flip_Flop #(.trigger("rising")) d_ff_2 (
    .clk(and_1_out), .D(load), .Q(d_ff_2_q), .reset(CLR));  // open: Qn, preset, en
  and and_1 (and_1_out, not_1_out, load);
  SHL shl_1 (.in_3(CLK_out), .in_4(d_ff_2_q), .in_5(CLR), .out_7(shl_1_out_7));  // open: in_2, in_1, out_6
  D_Flip_Flop #(.trigger("rising")) d_ff_3 (
    .clk(shl_1_out_7[2]), .D(adder_1_out), .Q(\output [2]), .reset(CLR));  // open: Qn, preset, en
  D_Flip_Flop #(.trigger("rising")) d_ff_4 (
    .clk(shl_1_out_7[1]), .D(adder_1_out), .Q(\output [1]), .reset(CLR));  // open: Qn, preset, en
  D_Flip_Flop #(.trigger("rising")) d_ff_5 (
    .clk(shl_1_out_7[0]), .D(adder_1_out), .Q(\output [0]), .reset(CLR));  // open: Qn, preset, en

  // Notes on the sheet:
  //   OPS: CLR - load - CLK (3)
endmodule

module SHL (
  input  in_1,
  input  [2:0] in_2,
  input  in_3,
  input  in_4,
  input  in_5,
  output out_6,
  output [2:0] out_7
);

  wire and_1_out, and_2_out, and_3_out;

  and and_1 (and_1_out, in_1, in_2[2]);
  and and_2 (and_2_out, in_1, in_2[1]);
  D_Flip_Flop #(.trigger("rising")) d_ff_1 (
    .clk(in_3), .D(out_7[1]), .Q(out_6), .preset(and_1_out), .reset(in_5));  // open: Qn, en
  and and_3 (and_3_out, in_1, in_2[0]);
  D_Flip_Flop #(.trigger("rising")) d_ff_2 (
    .clk(in_3), .D(out_7[0]), .Q(out_7[1]), .preset(and_2_out), .reset(in_5));  // open: Qn, en
  D_Flip_Flop #(.trigger("rising")) d_ff_3 (
    .clk(in_3), .D(in_4), .Q(out_7[0]), .preset(and_3_out), .reset(in_5));  // open: Qn, en

  assign out_7[2] = out_6;
endmodule

module SHR (
  input  in_1,
  input  [2:0] in_2,
  input  in_3,
  input  in_4,
  input  in_5,
  output out_6,
  output [2:0] out_7
);

  wire and_1_out, and_2_out, and_3_out;

  and and_1 (and_1_out, in_1, in_2[2]);
  and and_2 (and_2_out, in_1, in_2[1]);
  D_Flip_Flop #(.trigger("rising")) d_ff_1 (
    .clk(in_3), .D(in_4), .Q(out_7[2]), .preset(and_1_out), .reset(in_5));  // open: Qn, en
  and and_3 (and_3_out, in_1, in_2[0]);
  D_Flip_Flop #(.trigger("rising")) d_ff_2 (
    .clk(in_3), .D(out_7[2]), .Q(out_7[1]), .preset(and_2_out), .reset(in_5));  // open: Qn, en
  D_Flip_Flop #(.trigger("rising")) d_ff_3 (
    .clk(in_3), .D(out_7[1]), .Q(out_6), .preset(and_3_out), .reset(in_5));  // open: Qn, en

  assign out_7[0] = out_6;
endmodule
