// Logisim project main exercicioguia_05_03.circ as structural Verilog: 1 circuit, main circuit mainexercicioguia_05_03
module mainexercicioguia_05_03 (
  input  in_1,
  input  in_2
);

  wire and_1_out, and_2_out, not_1_out, not_2_out, or_1_out, undriven, undriven_2, undriven_3, xor_1_out;

  not not_1 (not_1_out, undriven);
  not not_2 (not_2_out, undriven_2);
  xor xor_1 (xor_1_out, undriven_2, undriven);
  and and_1 (and_1_out, undriven_2, not_1_out);
  nor nor_1 (not_1_out, undriven_3, undriven_3, not_2_out);
  and and_2 (and_2_out, undriven, undriven_2);
  or or_1 (or_1_out, and_1_out, and_2_out);

  // Notes on the sheet:
  //   NAO PODE ! E' CURTO-CIRCUITO !
  //    COLOCAR AS SAIDAS
endmodule
