// Logisim project maincircuito smacompleta02.circ as structural Verilog: 1 circuit, main circuit maincircuito somacompleta02
module maincircuito_somacompleta02 (
  input  in_1,
  input  in_2
);

  wire and_1_out, and_2_out, not_1_out, not_2_out, or_1_out, undriven, undriven_2, xor_1_out, xor_2_out;

  not not_1 (not_1_out, undriven);
  not not_2 (not_2_out, undriven);
  xor xor_1 (xor_1_out, undriven_2, undriven);
  and and_1 (and_1_out, undriven_2, not_1_out, xor_2_out);
  xor xor_2 (xor_2_out, undriven_2, undriven);
  and and_2 (and_2_out, undriven_2, not_2_out);
  or or_1 (or_1_out, and_1_out, and_2_out);
endmodule
