// Logisim project maincircuito somacompleta01.circ as structural Verilog: 1 circuit, main circuit maincircuito somacompleta01
module maincircuito_somacompleta01 (
  input  in_1,
  input  in_2,
  input  in_3
);

  wire and_1_out, and_2_out, not_1_out, or_1_out, undriven, undriven_2, xor_1_out, xor_2_out;

  not not_1 (not_1_out, undriven_2);
  ExactlyOne xor_1 (.out(xor_1_out), .in0(undriven), .in1(in_2), .in2(undriven_2), .in4(undriven_2));
  and and_1 (and_1_out, undriven, undriven_2, undriven_2);
  ExactlyOne xor_2 (.out(xor_2_out), .in0(undriven), .in2(undriven_2), .in3(undriven_2));
  and and_2 (and_2_out, not_1_out, undriven_2, undriven_2, undriven);
  or or_1 (or_1_out, xor_2_out, and_1_out, and_2_out);
endmodule
