// Logisim project Exemplo 02.circ as structural Verilog: 3 circuits, main circuit circuito
module circuito (
  input  a0,
  input  b0,
  input  a1,
  input  b1,
  output s0,
  output s1,
  output s2
);

  wire subcircuitomeia_1_s1;

  subCircuitoMeia subcircuitomeia_1 (.a(a0), .b(b0), .s0(s0), .s1(subcircuitomeia_1_s1));
  subCircuitoComp subcircuitocomp_1 (.c(subcircuitomeia_1_s1), .a(a1), .b(b1), .s0(s1), .s1(s2));
endmodule

module subCircuitoMeia (
  input  a,
  input  b,
  output s0,
  output s1
);

  wire not_1_out;

  not not_1 (not_1_out, a);
  xor xor_1 (s0, a, b);
  and and_1 (s1, b, not_1_out);
endmodule

module subCircuitoComp (
  input  c,
  input  a,
  input  b,
  output s0,
  output s1
);

  wire subcircuitomeia_1_s0, subcircuitomeia_1_s1, subcircuitomeia_2_s1;

  subCircuitoMeia subcircuitomeia_1 (.a(a), .b(b), .s0(subcircuitomeia_1_s0), .s1(subcircuitomeia_1_s1));
  subCircuitoMeia subcircuitomeia_2 (.a(subcircuitomeia_1_s0), .b(c), .s0(s0), .s1(subcircuitomeia_2_s1));
  or or_1 (s1, subcircuitomeia_2_s1, subcircuitomeia_1_s1);
endmodule
