// Logisim project Circ05_01.circ as structural Verilog: 2 circuits, main circuit main
module main (
  input  in_1,
  input  in_2,
  input  in_3,
  output out_4,
  output out_5
);

  wire meia_soma_1_out_3, meia_soma_1_out_4, meia_soma_2_out_4;

  meia_soma meia_soma_1 (.in_1(in_2), .in_2(in_3), .out_3(meia_soma_1_out_3), .out_4(meia_soma_1_out_4));
  meia_soma meia_soma_2 (.in_1(in_1), .in_2(meia_soma_1_out_3), .out_3(out_4), .out_4(meia_soma_2_out_4));
  or or_1 (out_5, meia_soma_2_out_4, meia_soma_1_out_4);
endmodule

module meia_soma (
  input  in_1,
  input  in_2,
  output out_3,
  output out_4
);

  and and_1 (out_4, in_2, in_2, in_1);
  xor xor_1 (out_3, in_1, in_2);
endmodule
