// Logisim project Circ05_02.circ as structural Verilog: 2 circuits, main circuit main
module main (
  input  in_1,
  input  in_2,
  input  in_3,
  output out_4,
  output out_5
);

  wire meia_diferenca_1_out_3, meia_diferenca_1_out_4, meia_diferenca_2_out_4;

  meia_diferenca meia_diferenca_1 (
    .in_1(in_2), .in_2(in_3), .out_3(meia_diferenca_1_out_3), .out_4(meia_diferenca_1_out_4));
  meia_diferenca meia_diferenca_2 (
    .in_1(meia_diferenca_1_out_3), .in_2(in_1), .out_3(out_4), .out_4(meia_diferenca_2_out_4));
  or or_1 (out_5, meia_diferenca_2_out_4, meia_diferenca_1_out_4);
endmodule

module meia_diferenca (
  input  in_1,
  input  in_2,
  output out_3,
  output out_4
);

  wire not_1_out;

  not not_1 (not_1_out, in_1);
  xor xor_1 (out_3, in_1, in_2);
  and and_1 (out_4, in_2, not_1_out);
endmodule
