// Logisim project Circ05_03.circ as structural Verilog: 1 circuit, main circuit main
module main (
  input  a,
  input  b,
  input  c,
  input  d,
  output s3,
  output s2,
  output s1,
  output s0
);

  wire and_1_out, and_2_out, and_3_out, and_4_out, and_5_out, and_6_out, and_7_out, and_8_out, and_11_out,
       and_12_out, and_13_out, and_14_out, and_15_out, and_16_out, not_1_out, not_2_out, not_3_out,
       not_4_out, not_5_out, not_6_out, or_2_out, or_3_out;

  and and_1 (and_1_out, a, b);
  and and_2 (and_2_out, c, d);
  and and_3 (and_3_out, a, not_1_out);
  not not_1 (not_1_out, b);
  and and_4 (and_4_out, a, c);
  not not_2 (not_2_out, d);
  not not_3 (not_3_out, a);
  and and_5 (and_5_out, not_3_out, b);
  and and_6 (and_6_out, b, c);
  not not_4 (not_4_out, d);
  and and_7 (and_7_out, a, not_5_out);
  not not_5 (not_5_out, b);
  and and_8 (and_8_out, a, not_6_out);
  not not_6 (not_6_out, c);
  and and_9 (s0, b, d);
  and and_10 (s3, and_1_out, and_2_out);
  and and_11 (and_11_out, and_3_out, c);
  and and_12 (and_12_out, and_4_out, not_2_out);
  and and_13 (and_13_out, and_5_out, c);
  and and_14 (and_14_out, and_6_out, not_4_out);
  and and_15 (and_15_out, and_7_out, d);
  and and_16 (and_16_out, and_8_out, d);
  or or_1 (s2, and_11_out, and_12_out);
  or or_2 (or_2_out, and_13_out, and_14_out);
  or or_3 (or_3_out, and_15_out, and_16_out);
  or or_4 (s1, or_2_out, or_3_out);
endmodule
