// Logisim project Guia0501.circ as structural Verilog: 3 circuits, main circuit HalfAdder
module HalfAdder (
  input  a,
  input  b,
  output s0,
  output s1
);

  xor xor_1 (s0, a, b);
  and and_1 (s1, b, a);
endmodule

module FullAdder (
  input  a,
  input  b,
  input  c,
  output s0,
  output s1
);

  wire halfadder_1_s1, halfadder_2_s0, halfadder_2_s1;

  HalfAdder halfadder_1 (.a(halfadder_2_s0), .b(c), .s0(s0), .s1(halfadder_1_s1));
  HalfAdder halfadder_2 (.a(a), .b(b), .s0(halfadder_2_s0), .s1(halfadder_2_s1));
  or or_1 (s1, halfadder_1_s1, halfadder_2_s1);

  // Notes on the sheet:
  //   Andre Sulivam 391998
endmodule

module Operador (
  input  g,
  input  a,
  input  b,
  input  c,
  input  d,
  input  e,
  input  f,
  output s0,
  output s1,
  output s2,
  output s3
);

  wire fulladder_1_s1, fulladder_2_s1, xor_1_out, xor_2_out, xor_3_out;

  xor xor_1 (xor_1_out, g, b);
  xor xor_2 (xor_2_out, g, d);
  xor xor_3 (xor_3_out, g, f);
  FullAdder fulladder_1 (.a(g), .b(xor_1_out), .c(a), .s0(s0), .s1(fulladder_1_s1));
  FullAdder fulladder_2 (.a(xor_2_out), .b(fulladder_1_s1), .c(c), .s0(s1), .s1(fulladder_2_s1));
  FullAdder fulladder_3 (.a(e), .b(xor_3_out), .c(fulladder_2_s1), .s0(s2), .s1(s3));
endmodule
