// Logisim project Guia0502.circ as structural Verilog: 3 circuits, main circuit Meia - Diferença
module \Meia___Diferença  (
  input  a,
  input  b,
  output s0,
  output s1
);

  wire not_1_out;

  not not_1 (not_1_out, a);
  and and_1 (s1, not_1_out, b);
  xor xor_1 (s0, a, b);

  // Notes on the sheet:
  //   Andre Sulivam 391998
endmodule

module \Diferença_Completa  (
  input  a,
  input  b,
  input  c,
  output s0,
  output s1
);

  wire \meia_diferença_1_s0 , \meia_diferença_1_s1 , \meia_diferença_2_s1 ;

  \Meia___Diferença  \meia_diferença_1  (.a(a), .b(b), .s0(\meia_diferença_1_s0 ), .s1(\meia_diferença_1_s1 ));
  \Meia___Diferença  \meia_diferença_2  (.a(\meia_diferença_1_s0 ), .b(c), .s0(s0), .s1(\meia_diferença_2_s1 ));
  or or_1 (s1, \meia_diferença_2_s1 , \meia_diferença_1_s1 );

  // Notes on the sheet:
  //   M.D
  //   M.D
endmodule

module \Diferença_Completa_dois_bits  (
  input  a0,
  input  b0,
  input  a1,
  input  b1,
  output s0,
  output s2,
  output s1
);

  wire \meia_diferença_1_s1 ;

  \Meia___Diferença  \meia_diferença_1  (.a(a0), .b(b0), .s0(s0), .s1(\meia_diferença_1_s1 ));
  \Diferença_Completa  \diferença_completa_1  (.a(\meia_diferença_1_s1 ), .b(a1), .c(b1), .s0(s2), .s1(s1));

  // Notes on the sheet:
  //   M.D
  //   D.C
endmodule
