// Logisim project Guia0503.circ as structural Verilog: 2 circuits, main circuit Meia-Soma
module Meia_Soma (
  input  a,
  input  b,
  output s0,
  output s1
);

  xor xor_1 (s0, a, b);
  and and_1 (s1, a, b);
endmodule

module Produto_2_bits (
  input  a1,
  input  a2,
  input  b1,
  input  b2,
  output s0,
  output s1,
  output s2,
  output s3
);

  wire and_2_out, and_3_out, and_4_out, meia_soma_1_s1;

  and and_1 (s0, a2, b2);
  and and_2 (and_2_out, a1, b2);
  and and_3 (and_3_out, a2, b1);
  and and_4 (and_4_out, b1, a1);
  Meia_Soma meia_soma_1 (.a(and_2_out), .b(and_3_out), .s0(s1), .s1(meia_soma_1_s1));
  Meia_Soma meia_soma_2 (.a(meia_soma_1_s1), .b(and_4_out), .s0(s2), .s1(s3));

  // Notes on the sheet:
  //   X
  //   Andre Sulivam 391998
  //   M.S
  //   M.S
endmodule
