// Logisim project ex501.circ as structural Verilog: 3 circuits, main circuit Soma-Completa
module Meia_Soma (
  input  a,
  input  b,
  output s0,
  output s1
);

  xor xor_1 (s0, a, b);
  and and_1 (s1, a, b);

  // Notes on the sheet:
  //   Meia-Soma
endmodule

module Soma_Completa (
  input  carry_in,
  input  a,
  input  b,
  output s0,
  output carry_out
);

  wire meia_soma_1_s0, meia_soma_1_s1, meia_soma_2_s1;

  Meia_Soma meia_soma_1 (.a(a), .b(b), .s0(meia_soma_1_s0), .s1(meia_soma_1_s1));
  Meia_Soma meia_soma_2 (.a(carry_in), .b(meia_soma_1_s0), .s0(s0), .s1(meia_soma_2_s1));
  or or_1 (carry_out, meia_soma_2_s1, meia_soma_1_s1);

  // Notes on the sheet:
  //   Soma - Completa
endmodule

module Soma_Completa_3_bits (
  input  a2,
  input  a1,
  input  a0,
  input  b1,
  input  b1_2,
  input  b0,
  output s3,
  output s2,
  output s1,
  output s0
);

  wire meia_soma_1_s1, soma_completa_1_carry_out;

  Meia_Soma meia_soma_1 (.a(a0), .b(b0), .s0(s0), .s1(meia_soma_1_s1));
  Soma_Completa soma_completa_1 (
    .carry_in(meia_soma_1_s1), .a(a1), .b(b1_2), .s0(s1), .carry_out(soma_completa_1_carry_out));
  Soma_Completa soma_completa_2 (.carry_in(soma_completa_1_carry_out), .a(a2), .b(b1), .s0(s2), .carry_out(s3));
endmodule
