// Logisim project ex502.circ as structural Verilog: 3 circuits, main circuit MeiaDiferenca
module MeiaDiferenca (
  input  a,
  input  b,
  output d,
  output v
);

  wire not_1_out;

  not not_1 (not_1_out, a);
  xor xor_1 (d, a, b);
  and and_1 (v, not_1_out, b);

  // Notes on the sheet:
  //   Meia Diferença
endmodule

module diferencaCompleta (
  input  vem_um,
  input  a,
  input  b,
  output s0,
  output s1
);

  wire meiadiferenca_1_d, meiadiferenca_1_v, meiadiferenca_2_v;

  MeiaDiferenca meiadiferenca_1 (.a(a), .b(b), .d(meiadiferenca_1_d), .v(meiadiferenca_1_v));
  MeiaDiferenca meiadiferenca_2 (.a(meiadiferenca_1_d), .b(vem_um), .d(s0), .v(meiadiferenca_2_v));
  or or_1 (s1, meiadiferenca_2_v, meiadiferenca_1_v);

  // Notes on the sheet:
  //   Diferenca Completa
endmodule

module \Diferença_2bits  (
  input  a1,
  input  a0,
  input  b1,
  input  b0,
  output s1,
  output s0
);

  wire meiadiferenca_1_v;

  MeiaDiferenca meiadiferenca_1 (.a(a0), .b(b0), .d(s0), .v(meiadiferenca_1_v));
  diferencaCompleta diferencacompleta_1 (.vem_um(meiadiferenca_1_v), .a(a1), .b(b1), .s0(s1));  // open: s1

  // Notes on the sheet:
  //   Diferença Completa 2bits
endmodule
