// Logisim project ex503.circ as structural Verilog: 6 circuits, main circuit Soma-Completa
module Meia_Soma (
  input  a,
  input  b,
  output s0,
  output s1
);

  xor xor_1 (s0, a, b);
  and and_1 (s1, a, b);

  // Notes on the sheet:
  //   Meia-Soma
endmodule

module Soma_Completa (
  input  carry_in,
  input  a,
  input  b,
  output s0,
  output carry_out
);

  wire meia_soma_1_s0, meia_soma_1_s1, meia_soma_2_s1;

  Meia_Soma meia_soma_1 (.a(a), .b(b), .s0(meia_soma_1_s0), .s1(meia_soma_1_s1));
  Meia_Soma meia_soma_2 (.a(carry_in), .b(meia_soma_1_s0), .s0(s0), .s1(meia_soma_2_s1));
  or or_1 (carry_out, meia_soma_2_s1, meia_soma_1_s1);

  // Notes on the sheet:
  //   Soma - Completa
endmodule

module Soma_Completa_3_bits (
  input  a2,
  input  a1,
  input  a0,
  input  b1,
  input  b1_2,
  input  b0,
  output s3,
  output s2,
  output s1,
  output s0
);

  wire meia_soma_1_s1, soma_completa_1_carry_out;

  Meia_Soma meia_soma_1 (.a(a0), .b(b0), .s0(s0), .s1(meia_soma_1_s1));
  Soma_Completa soma_completa_1 (
    .carry_in(meia_soma_1_s1), .a(a1), .b(b1_2), .s0(s1), .carry_out(soma_completa_1_carry_out));
  Soma_Completa soma_completa_2 (.carry_in(soma_completa_1_carry_out), .a(a2), .b(b1), .s0(s2), .carry_out(s3));
endmodule

module Produto (
  input  a1,
  input  a0,
  input  b1,
  input  b0,
  input  in_5,
  input  in_6,
  output s3,
  output s2,
  output s1,
  output s0
);

  wire and_1_out, and_2_out, and_3_out, and_4_out, meia_soma_1_s1, soma_completa_1_carry_out;

  and and_1 (and_1_out, b0, a0);
  and and_2 (and_2_out, b0, a1);
  and and_3 (and_3_out, b1, a0);
  and and_4 (and_4_out, b1, a1);
  Meia_Soma meia_soma_1 (.a(in_5), .b(and_1_out), .s0(s0), .s1(meia_soma_1_s1));
  Soma_Completa soma_completa_1 (
    .carry_in(meia_soma_1_s1), .a(and_2_out), .b(and_3_out), .s0(s1), .carry_out(soma_completa_1_carry_out));
  Soma_Completa soma_completa_2 (
    .carry_in(soma_completa_1_carry_out), .a(and_4_out), .b(in_6), .s0(s2), .carry_out(s3));
endmodule

module produto_p (
  input  carry_in,
  input  e0,
  input  e1,
  input  e2,
  input  e3,
  output s0,
  output carry_out
);

  wire and_1_out, and_2_out;

  and and_1 (and_1_out, e0, e1);
  and and_2 (and_2_out, e2, e3);
  Soma_Completa soma_completa_1 (.carry_in(carry_in), .a(and_1_out), .b(and_2_out), .s0(s0), .carry_out(carry_out));

  // Notes on the sheet:
  //   Produto
endmodule

module Produto_Completo (
  input  a1,
  input  a0,
  input  b1,
  input  b0,
  input  in_5,
  input  in_6,
  output s3,
  output s2,
  output s1,
  output s0
);

  wire produto_p_1_carry_out, produto_p_2_carry_out;

  produto_p produto_p_1 (
    .e0(in_5), .e1(in_5), .e2(a0), .e3(b0), .carry_in(in_5), .s0(s0), .carry_out(produto_p_1_carry_out));
  produto_p produto_p_2 (
    .e0(a0), .e1(b1), .e2(a1), .e3(b0), .carry_in(produto_p_1_carry_out), .s0(s1),
    .carry_out(produto_p_2_carry_out));
  produto_p produto_p_3 (
    .e0(b1), .e1(a1), .e2(in_6), .e3(in_6), .carry_in(produto_p_2_carry_out), .s0(s2), .carry_out(s3));

  // Notes on the sheet:
  //   Produto Completo
endmodule
