// Logisim project ex504.circ as structural Verilog
module Meia_Soma (
  input  a,
  input  b,
  output s0,
  output s1
);

  wire nand_1_out, nand_2_out, nand_3_out, nand_4_out, nand_6_out, nand_7_out;

  nand nand_1 (nand_1_out, a, a);
  nand nand_2 (nand_2_out, b, b);
  nand nand_3 (nand_3_out, a, b);
  nand nand_4 (nand_4_out, nand_1_out, nand_2_out);
  nand nand_5 (s1, nand_3_out, nand_3_out);
  nand nand_6 (nand_6_out, s1, s1);
  nand nand_7 (nand_7_out, nand_4_out, nand_6_out);
  nand nand_8 (s0, nand_7_out, nand_7_out);

  // Notes on the sheet:
  //   Meia Soma
  //   Celso R Franca Jr
endmodule

module Soma_Completa (
  input  carry_in,
  input  a,
  input  b,
  output s0,
  output s1
);

  wire meia_soma_1_s0, meia_soma_1_s1, meia_soma_2_s1, nand_1_out, nand_2_out;

  Meia_Soma meia_soma_1 (.a(a), .b(b), .s0(meia_soma_1_s0), .s1(meia_soma_1_s1));
  Meia_Soma meia_soma_2 (.a(carry_in), .b(meia_soma_1_s0), .s0(s0), .s1(meia_soma_2_s1));
  nand nand_1 (nand_1_out, meia_soma_2_s1, meia_soma_2_s1);
  nand nand_2 (nand_2_out, meia_soma_1_s1, meia_soma_1_s1);
  nand nand_3 (s1, nand_1_out, nand_2_out);

  // Notes on the sheet:
  //   Soma-Completa
endmodule

module Soma_2bits (
  input  a1,
  input  a0,
  input  b1,
  input  b0,
  output out_5,
  output out_6,
  output out_7
);

  wire meia_soma_1_s1;

  Meia_Soma meia_soma_1 (.a(b0), .b(a0), .s0(out_7), .s1(meia_soma_1_s1));
  Soma_Completa soma_completa_1 (.carry_in(meia_soma_1_s1), .a(b1), .b(a1), .s0(out_6), .s1(out_5));
endmodule
