// Logisim project ex505.circ as structural Verilog: 3 circuits, main circuit MeiaDiferenca
module MeiaDiferenca (
  input  a,
  input  b,
  output d,
  output v
);

  wire nor_1_out, nor_2_out, nor_3_out, nor_4_out, nor_5_out;

  nor nor_1 (nor_1_out, a, b);
  nor nor_2 (nor_2_out, a, nor_1_out);
  nor nor_3 (nor_3_out, nor_1_out, b);
  nor nor_4 (nor_4_out, b, b);
  nor nor_5 (nor_5_out, nor_2_out, nor_3_out);
  nor nor_6 (v, a, nor_4_out);
  nor nor_7 (d, nor_5_out, nor_5_out);

  // Notes on the sheet:
  //   Meia Diferenca
endmodule

module difCompleta (
  input  vem_um,
  input  a,
  input  b,
  output s0,
  output s1
);

  wire meiadiferenca_1_d, meiadiferenca_1_v, meiadiferenca_2_v, nor_1_out;

  MeiaDiferenca meiadiferenca_1 (.a(a), .b(b), .d(meiadiferenca_1_d), .v(meiadiferenca_1_v));
  MeiaDiferenca meiadiferenca_2 (.a(meiadiferenca_1_d), .b(vem_um), .d(s0), .v(meiadiferenca_2_v));
  nor nor_1 (nor_1_out, meiadiferenca_2_v, meiadiferenca_1_v);
  nor nor_2 (s1, nor_1_out, nor_1_out);

  // Notes on the sheet:
  //   Diferenca Completa
endmodule

module Diferenca_2bits (
  input  a1,
  input  a0,
  input  b1,
  input  b0,
  output out_5,
  output out_6
);

  wire meiadiferenca_1_v;

  MeiaDiferenca meiadiferenca_1 (.a(a0), .b(b0), .d(out_6), .v(meiadiferenca_1_v));
  difCompleta difcompleta_1 (.vem_um(meiadiferenca_1_v), .a(a1), .b(b1), .s0(out_5));  // open: s1
endmodule
