// Logisim project Circuitos.circ as structural Verilog: 8 circuits, main circuit Meia-Soma(Comum)
module Meia_Soma_Comum (
  input  a,
  input  b,
  output S0,
  output S1
);

  wire and_1_out, and_2_out, not_1_out, not_2_out;

  not not_1 (not_1_out, a);
  not not_2 (not_2_out, b);
  and and_1 (and_1_out, not_1_out, b);
  and and_2 (and_2_out, a, not_2_out);
  and and_3 (S1, a, b);
  or or_1 (S0, and_1_out, and_2_out);
endmodule

module somaCompleta_Comum (
  input  a,
  input  b,
  input  c,
  output S0,
  output S1
);

  wire meia_soma_comum_1_s0, meia_soma_comum_1_s1, meia_soma_comum_2_s1;

  Meia_Soma_Comum meia_soma_comum_1 (.a(a), .b(b), .S0(meia_soma_comum_1_s0), .S1(meia_soma_comum_1_s1));
  Meia_Soma_Comum meia_soma_comum_2 (.a(meia_soma_comum_1_s0), .b(c), .S0(S0), .S1(meia_soma_comum_2_s1));
  or or_1 (S1, meia_soma_comum_2_s1, meia_soma_comum_1_s1);
endmodule

module \Meia_Difereça_Comum  (
  input  a,
  input  b,
  output S0,
  output S1
);

  wire and_1_out, and_2_out, not_1_out, not_2_out, not_3_out;

  not not_1 (not_1_out, a);
  not not_2 (not_2_out, b);
  not not_3 (not_3_out, a);
  and and_1 (and_1_out, not_1_out, b);
  and and_2 (and_2_out, a, not_2_out);
  and and_3 (S1, not_3_out, b);
  or or_1 (S0, and_1_out, and_2_out);
endmodule

module \diferençaCompleta  (
  input  a,
  input  b,
  input  c,
  output S0,
  output S1
);

  wire \meia_difereça_comum_1_s0 , \meia_difereça_comum_1_s1 , \meia_difereça_comum_2_s1 ;

  \Meia_Difereça_Comum  \meia_difereça_comum_1  (
    .a(a), .b(b), .S0(\meia_difereça_comum_1_s0 ), .S1(\meia_difereça_comum_1_s1 ));
  \Meia_Difereça_Comum  \meia_difereça_comum_2  (
    .a(\meia_difereça_comum_1_s0 ), .b(c), .S0(S0), .S1(\meia_difereça_comum_2_s1 ));
  or or_1 (S1, \meia_difereça_comum_2_s1 , \meia_difereça_comum_1_s1 );
endmodule

module meiaSoma_Nor (
  input  a,
  input  b,
  output S0,
  output S1
);

  wire nor_1_out, nor_2_out, nor_3_out, nor_4_out, nor_5_out, nor_6_out;

  nor nor_1 (nor_1_out, a, a);
  nor nor_2 (nor_2_out, b, b);
  nor nor_3 (nor_3_out, a, b);
  nor nor_4 (nor_4_out, a, a);
  nor nor_5 (nor_5_out, b, b);
  nor nor_6 (nor_6_out, nor_1_out, nor_2_out);
  nor nor_7 (S1, nor_4_out, nor_5_out);
  nor nor_8 (S0, nor_6_out, nor_3_out);
endmodule

module Somador_3bits (
  input  a2,
  input  a1,
  input  a0,
  input  b2,
  input  b1,
  input  b0,
  input  in_7,
  output S0,
  output S1,
  output S2,
  output S3
);

  wire somacompleta_comum_1_s1, somacompleta_comum_2_s1;

  somaCompleta_Comum somacompleta_comum_1 (.a(a0), .b(b0), .c(in_7), .S0(S0), .S1(somacompleta_comum_1_s1));
  somaCompleta_Comum somacompleta_comum_2 (
    .a(a1), .b(b1), .c(somacompleta_comum_1_s1), .S0(S1), .S1(somacompleta_comum_2_s1));
  somaCompleta_Comum somacompleta_comum_3 (.a(a2), .b(b2), .c(somacompleta_comum_2_s1), .S0(S2), .S1(S3));
endmodule

module Subtrator_2bits (
  input  a1,
  input  a0,
  input  b1,
  input  b0,
  input  in_5,
  output S0,
  output S1,
  output S2
);

  wire \diferençacompleta_1_s1 ;

  \diferençaCompleta  \diferençacompleta_1  (.a(a0), .b(b0), .c(in_5), .S0(S0), .S1(\diferençacompleta_1_s1 ));
  \diferençaCompleta  \diferençacompleta_2  (.a(a1), .b(b1), .c(\diferençacompleta_1_s1 ), .S0(S1), .S1(S2));
endmodule

module Multiplicador_2bits (
  input  a1,
  input  a0,
  input  b1,
  input  b0,
  input  in_5,
  output S0,
  output S1,
  output S2,
  output S3
);

  wire and_2_out, and_3_out, and_4_out, meia_soma_comum_1_s1;

  and and_1 (S0, a0, b0);
  and and_2 (and_2_out, a0, b1);
  and and_3 (and_3_out, a1, b0);
  and and_4 (and_4_out, a1, b1);
  Meia_Soma_Comum meia_soma_comum_1 (.a(and_2_out), .b(and_3_out), .S0(S1), .S1(meia_soma_comum_1_s1));
  somaCompleta_Comum somacompleta_comum_1 (.a(and_4_out), .b(in_5), .c(meia_soma_comum_1_s1), .S0(S2), .S1(S3));
endmodule
