// Logisim project G5E1.circ as structural Verilog: 3 circuits, main circuit Full-Adder
module Full_Adder (
  input  Carry_in,
  input  a,
  input  b,
  output s0,
  output Carry_out
);

  wire half_adder_1_s0, half_adder_1_s1__carry, half_adder_2_s1__carry;

  Half_Adder half_adder_1 (.a(Carry_in), .b(a), .s0(half_adder_1_s0), .s1__carry(half_adder_1_s1__carry));
  Half_Adder half_adder_2 (.a(half_adder_1_s0), .b(b), .s0(s0), .s1__carry(half_adder_2_s1__carry));
  or or_1 (Carry_out, half_adder_2_s1__carry, half_adder_1_s1__carry);

  // Notes on the sheet:
  //   Nome: Alan Diniz Nogueira Machado
  //   Matrícula:405782
  //   Guia 05_01 - Somador Completo com Portas XOR e AND
endmodule

module Half_Adder (
  input  a,
  input  b,
  output s0,
  output s1__carry
);

  xor xor_1 (s0, a, b);
  and and_1 (s1__carry, b, a);

  // Notes on the sheet:
  //   Matrícula:405782
  //   Nome: Alan Diniz Nogueira Machado
  //   Guia 05_01 - Meio Somador com Portas XOR e AND
endmodule

module ULA___3bits (
  input  [2:0] Number_1,
  input  [2:0] Number_2,
  output [2:0] Result,
  output out_4
);

  wire full_adder_1_carry_out, half_adder_1_s1__carry;

  Half_Adder half_adder_1 (.a(Number_1[0]), .b(Number_2[0]), .s0(Result[0]), .s1__carry(half_adder_1_s1__carry));
  Full_Adder full_adder_1 (
    .Carry_in(half_adder_1_s1__carry), .a(Number_1[1]), .b(Number_2[1]), .s0(Result[1]),
    .Carry_out(full_adder_1_carry_out));
  Full_Adder full_adder_2 (
    .Carry_in(full_adder_1_carry_out), .a(Number_1[2]), .b(Number_2[2]), .s0(Result[2]), .Carry_out(out_4));

  // Notes on the sheet:
  //   Guia 05_01 - Somador de 3bits
  //   Nome: Alan Diniz Nogueira Machado
  //   Matrícula: 405782
endmodule
