// Logisim project G5E2.circ as structural Verilog: 3 circuits, main circuit Half-Subtractor
module Half_Subtractor (
  input  a,
  input  b,
  output s0,
  output s1__borrow
);

  wire not_1_out;

  not not_1 (not_1_out, a);
  xor xor_1 (s0, a, b);
  and and_1 (s1__borrow, b, not_1_out);

  // Notes on the sheet:
  //   Nome: Alan Diniz Nogueira Machado
  //   Matrícula:405782
  //   Guia 05_02 - Meio Subtrator com Portas XOR e AND
endmodule

module Full_Subtractor (
  input  a,
  input  b,
  input  Borrow_In,
  output s0,
  output Borrow_out
);

  wire half_subtractor_1_s0, half_subtractor_1_s1__borrow, half_subtractor_2_s1__borrow;

  Half_Subtractor half_subtractor_1 (
    .a(a), .b(b), .s0(half_subtractor_1_s0), .s1__borrow(half_subtractor_1_s1__borrow));
  Half_Subtractor half_subtractor_2 (
    .a(half_subtractor_1_s0), .b(Borrow_In), .s0(s0), .s1__borrow(half_subtractor_2_s1__borrow));
  or or_1 (Borrow_out, half_subtractor_2_s1__borrow, half_subtractor_1_s1__borrow);

  // Notes on the sheet:
  //   Nome: Alan Diniz Nogueira Machado
  //   Matrícula:405782
  //   Guia 05_02 - Subtrator Completo com Portas XOR e AND
endmodule

module ULA___2bits (
  input  [1:0] Number_1,
  input  [1:0] Number_2,
  output [1:0] Result,
  output out_4
);

  wire half_subtractor_1_s1__borrow;

  Half_Subtractor half_subtractor_1 (
    .a(Number_1[0]), .b(Number_2[0]), .s0(Result[0]), .s1__borrow(half_subtractor_1_s1__borrow));
  Full_Subtractor full_subtractor_1 (
    .a(Number_1[1]), .b(Number_2[1]), .Borrow_In(half_subtractor_1_s1__borrow), .s0(Result[1]),
    .Borrow_out(out_4));

  // Notes on the sheet:
  //   Guia 05_02 - Subtrator de 2bits
  //   Nome: Alan Diniz Nogueira Machado
  //   Matrícula: 405782
endmodule
