// Logisim project G5E3.circ as structural Verilog: 2 circuits, main circuit Half-Adder
module Half_Adder (
  input  a,
  input  b,
  output s0,
  output s1__carry
);

  xor xor_1 (s0, a, b);
  and and_1 (s1__carry, b, a);

  // Notes on the sheet:
  //   Matrícula:405782
  //   Nome: Alan Diniz Nogueira Machado
  //   Guia 05_03 - Meio Somador com Portas XOR e AND
endmodule

module Full_Multiplier (
  input  [1:0] Number_1,
  input  [1:0] Number_2,
  output [3:0] result
);

  wire and_2_out, and_3_out, and_4_out, half_adder_1_s1__carry;

  and and_1 (result[0], Number_1[0], Number_2[0]);
  and and_2 (and_2_out, Number_2[0], Number_1[1]);
  and and_3 (and_3_out, Number_1[0], Number_2[1]);
  and and_4 (and_4_out, Number_1[1], Number_2[1]);
  Half_Adder half_adder_1 (.a(and_2_out), .b(and_3_out), .s0(result[1]), .s1__carry(half_adder_1_s1__carry));
  Half_Adder half_adder_2 (.a(half_adder_1_s1__carry), .b(and_4_out), .s0(result[2]), .s1__carry(result[3]));

  // Notes on the sheet:
  //   Matrícula:405782
  //   Guia 05_03 - Multiplicador Completo
  //   Nome: Alan Diniz Nogueira Machado
endmodule
