// Logisim project Juss.circ as structural Verilog: 4 circuits, main circuit main
module main (
  input  in_1,
  input  in_2,
  input  in_3,
  input  in_4,
  input  in_5,
  input  in_6,
  input  in_7,
  input  in_8,
  input  in_9,
  input  in_10,
  input  in_11,
  input  in_12,
  input  in_13,
  output out_14,
  output out_15,
  output out_16,
  output Primeiro_valor,
  output out_18,
  output out_19,
  output out_20,
  output out_21
);

  wire somacompleta_1_out_5, somacompleta_2_out_5;

  SomaCompleta somacompleta_1 (.in_1(in_7), .in_2(in_8), .in_3(in_9), .out_4(out_18), .out_5(somacompleta_1_out_5));
  SomaCompleta somacompleta_2 (
    .in_1(somacompleta_1_out_5), .in_2(in_10), .in_3(in_11), .out_4(out_19), .out_5(somacompleta_2_out_5));
  SomaCompleta somacompleta_3 (.in_1(somacompleta_2_out_5), .in_2(in_12), .in_3(in_13), .out_4(out_20), .out_5(out_21));
  Exercicio01 exercicio01_1 (
    .a0(in_3), .b0(in_6), .a1(in_2), .b1(in_5), .a2(in_1), .b2(in_4), .s0(Primeiro_valor), .s1(out_16),
    .s2(out_15), .s3(out_14));

  // Notes on the sheet:
  //   Soma completa de dois numeros de 3 bits cada
endmodule

module MeiaSoma (
  input  in_1,
  input  in_2,
  output out_3,
  output out_4
);

  xor xor_1 (out_3, in_1, in_2);
  and and_1 (out_4, in_1, in_2);
endmodule

module SomaCompleta (
  input  in_1,
  input  in_2,
  input  in_3,
  output out_4,
  output out_5
);

  wire meiasoma_1_out_3, meiasoma_1_out_4, meiasoma_2_out_4;

  MeiaSoma meiasoma_1 (.in_1(in_2), .in_2(in_3), .out_3(meiasoma_1_out_3), .out_4(meiasoma_1_out_4));
  MeiaSoma meiasoma_2 (.in_1(in_1), .in_2(meiasoma_1_out_3), .out_3(out_4), .out_4(meiasoma_2_out_4));
  or or_1 (out_5, meiasoma_2_out_4, meiasoma_1_out_4);
endmodule

module Exercicio01 (
  input  a0,
  input  b0,
  input  a1,
  input  b1,
  input  a2,
  input  b2,
  output s0,
  output s1,
  output s2,
  output s3
);

  wire meiasoma_1_out_4, somacompleta_1_out_5;

  MeiaSoma meiasoma_1 (.in_1(a0), .in_2(b0), .out_3(s0), .out_4(meiasoma_1_out_4));
  SomaCompleta somacompleta_1 (.in_1(meiasoma_1_out_4), .in_2(a1), .in_3(b1), .out_4(s1), .out_5(somacompleta_1_out_5));
  SomaCompleta somacompleta_2 (.in_1(somacompleta_1_out_5), .in_2(a2), .in_3(b2), .out_4(s2), .out_5(s3));
endmodule
