// Logisim project guia05.circ as structural Verilog: 13 circuits, main circuit half-adder
module half_adder (
  input  A,
  input  B,
  output s0,
  output s1
);

  wire not_1_out, or_1_out;

  or or_1 (or_1_out, A, B);
  and and_1 (s1, A, B);
  not not_1 (not_1_out, s1);
  and and_2 (s0, or_1_out, or_1_out, not_1_out);
endmodule

module full_adder (
  input  A,
  input  B,
  input  Cin,
  output s0,
  output s1
);

  wire half_adder_1_s0, half_adder_1_s1, half_adder_2_s1;

  half_adder half_adder_1 (.A(A), .B(B), .s0(half_adder_1_s0), .s1(half_adder_1_s1));
  half_adder half_adder_2 (.A(half_adder_1_s0), .B(Cin), .s0(s0), .s1(half_adder_2_s1));
  or or_1 (s1, half_adder_2_s1, half_adder_1_s1);
endmodule

module full_adder_3b (
  input  Cin,
  input  A,
  input  A1,
  input  B,
  input  B1,
  input  C,
  input  C1,
  output s0,
  output s1,
  output s2,
  output s3
);

  wire full_adder_1_s1, full_adder_2_s1;

  full_adder full_adder_1 (.A(A), .B(A1), .Cin(Cin), .s0(s0), .s1(full_adder_1_s1));
  full_adder full_adder_2 (.A(B), .B(B1), .Cin(full_adder_1_s1), .s0(s1), .s1(full_adder_2_s1));
  full_adder full_adder_3 (.A(C), .B(C1), .Cin(full_adder_2_s1), .s0(s2), .s1(s3));
endmodule

module half_subtractor (
  input  A,
  input  B,
  output s0,
  output s1
);

  wire not_1_out;

  xor xor_1 (s0, A, B);
  not not_1 (not_1_out, A);
  and and_1 (s1, not_1_out, B);
endmodule

module full_subtractor (
  input  A,
  input  B,
  input  Cin,
  output s0,
  output s1
);

  wire half_subtractor_1_s0, half_subtractor_1_s1, half_subtractor_2_s1;

  half_subtractor half_subtractor_1 (.A(A), .B(B), .s0(half_subtractor_1_s0), .s1(half_subtractor_1_s1));
  half_subtractor half_subtractor_2 (.A(half_subtractor_1_s0), .B(Cin), .s0(s0), .s1(half_subtractor_2_s1));
  or or_1 (s1, half_subtractor_2_s1, half_subtractor_1_s1);
endmodule

module Full_subtractor_2b (
  input  Cin,
  input  A,
  input  A1,
  input  B,
  input  B1,
  output s0,
  output s1,
  output s2
);

  wire full_subtractor_1_s1;

  full_subtractor full_subtractor_1 (.A(A), .B(A1), .Cin(Cin), .s0(s0), .s1(full_subtractor_1_s1));
  full_subtractor full_subtractor_2 (.A(B), .B(B1), .Cin(full_subtractor_1_s1), .s0(s1), .s1(s2));
endmodule

module \Multiplicação  (
  input  A,
  input  A1,
  input  B,
  input  B1,
  output s0,
  output s1,
  output s2,
  output s3
);

  wire and_2_out, and_3_out, and_4_out, half_adder_1_s1;

  and and_1 (s0, A, A1);
  and and_2 (and_2_out, A, B1);
  and and_3 (and_3_out, A1, B);
  and and_4 (and_4_out, B, B1);
  half_adder half_adder_1 (.A(and_2_out), .B(and_3_out), .s0(s1), .s1(half_adder_1_s1));
  half_adder half_adder_2 (.A(and_4_out), .B(half_adder_1_s1), .s0(s2), .s1(s3));
endmodule

module half_adder_nand (
  input  A,
  input  B,
  output s0,
  output s1
);

  wire nand_1_out, nand_2_out, nand_3_out, nand_4_out, nand_6_out, nand_7_out;

  nand nand_1 (nand_1_out, A, A);
  nand nand_2 (nand_2_out, B, B);
  nand nand_3 (nand_3_out, A, B);
  nand nand_4 (nand_4_out, nand_1_out, nand_2_out);
  nand nand_5 (s1, nand_3_out, nand_3_out);
  nand nand_6 (nand_6_out, s1, s1);
  nand nand_7 (nand_7_out, nand_4_out, nand_6_out);
  nand nand_8 (s0, nand_7_out, nand_7_out);
endmodule

module full_adder_nand (
  input  A,
  input  B,
  input  Cin,
  output s0,
  output s1
);

  wire half_adder_nand_1_s0, half_adder_nand_1_s1, half_adder_nand_2_s1, nand_1_out, nand_2_out;

  half_adder_nand half_adder_nand_1 (.A(A), .B(B), .s0(half_adder_nand_1_s0), .s1(half_adder_nand_1_s1));
  half_adder_nand half_adder_nand_2 (.A(half_adder_nand_1_s0), .B(Cin), .s0(s0), .s1(half_adder_nand_2_s1));
  nand nand_1 (nand_1_out, half_adder_nand_2_s1, half_adder_nand_2_s1);
  nand nand_2 (nand_2_out, half_adder_nand_1_s1, half_adder_nand_1_s1);
  nand nand_3 (s1, nand_1_out, nand_2_out);
endmodule

module full_adder_2b (
  input  Cin,
  input  A,
  input  A1,
  input  B,
  input  B1,
  output s0,
  output s1,
  output s2
);

  wire full_adder_nand_1_s1;

  full_adder_nand full_adder_nand_1 (.A(A), .B(A1), .Cin(Cin), .s0(s0), .s1(full_adder_nand_1_s1));
  full_adder_nand full_adder_nand_2 (.A(B), .B(B1), .Cin(full_adder_nand_1_s1), .s0(s1), .s1(s2));
endmodule

module half_subtractor_nor (
  input  A,
  input  B,
  output s0,
  output s1
);

  wire nor_1_out, nor_2_out, nor_3_out, nor_4_out, nor_5_out, nor_7_out;

  nor nor_1 (nor_1_out, B, B);
  nor nor_2 (nor_2_out, A, A);
  nor nor_3 (nor_3_out, B, B);
  nor nor_4 (nor_4_out, A, nor_1_out);
  nor nor_5 (nor_5_out, nor_2_out, B);
  nor nor_6 (s1, A, nor_3_out);
  nor nor_7 (nor_7_out, nor_4_out, nor_5_out);
  nor nor_8 (s0, nor_7_out, nor_7_out);
endmodule

module full_subtractor_nor (
  input  A,
  input  B,
  input  Cin,
  output s0,
  output s1
);

  wire half_subtractor_nor_1_s0, half_subtractor_nor_1_s1, half_subtractor_nor_2_s1;

  half_subtractor_nor half_subtractor_nor_1 (
    .A(A), .B(B), .s0(half_subtractor_nor_1_s0), .s1(half_subtractor_nor_1_s1));
  half_subtractor_nor half_subtractor_nor_2 (
    .A(half_subtractor_nor_1_s0), .B(Cin), .s0(s0), .s1(half_subtractor_nor_2_s1));
  or or_1 (s1, half_subtractor_nor_2_s1, half_subtractor_nor_1_s1);
endmodule

module full_subtractor_nor_2b (
  input  Cin,
  input  A,
  input  A1,
  input  B,
  input  B1,
  output s0,
  output s1,
  output s2
);

  wire full_subtractor_nor_1_s1;

  full_subtractor_nor full_subtractor_nor_1 (.A(A), .B(A1), .Cin(Cin), .s0(s0), .s1(full_subtractor_nor_1_s1));
  full_subtractor_nor full_subtractor_nor_2 (.A(B), .B(B1), .Cin(full_subtractor_nor_1_s1), .s0(s1), .s1(s2));
endmodule
