// Logisim project Multiplicador.circ as structural Verilog
module Multiplicador (
  input  a0,
  input  b0,
  input  a1,
  input  b1,
  output s0,
  output s1,
  output s2,
  output s3
);

  wire and_2_out, and_3_out, and_4_out, half_adder_1_carry_out;

  and and_1 (s0, a0, b0);
  and and_2 (and_2_out, a0, b1);
  and and_3 (and_3_out, b0, a1);
  and and_4 (and_4_out, a1, b1);
  Half_Adder half_adder_1 (.x(and_2_out), .y(and_3_out), .s0(s1), .Carry_Out(half_adder_1_carry_out));
  Half_Adder half_adder_2 (.x(and_4_out), .y(half_adder_1_carry_out), .s0(s2), .Carry_Out(s3));
endmodule

module Half_Adder (
  input  x,
  input  y,
  output s0,
  output Carry_Out
);

  wire not_1_out, or_1_out;

  or or_1 (or_1_out, y, x);
  and and_1 (Carry_Out, x, y);
  not not_1 (not_1_out, Carry_Out);
  and and_2 (s0, or_1_out, not_1_out);
endmodule
