// Logisim project Somador 3 bits.circ as structural Verilog
module Half_Adder (
  input  x,
  input  y,
  output s0,
  output Carry_Out
);

  wire not_1_out, or_1_out;

  or or_1 (or_1_out, y, x);
  and and_1 (Carry_Out, x, y);
  not not_1 (not_1_out, Carry_Out);
  and and_2 (s0, or_1_out, not_1_out);
endmodule

module Full_Adder (
  input  carry,
  input  x,
  input  y,
  output s0,
  output Carry_out
);

  wire half_adder_1_carry_out, half_adder_2_carry_out, half_adder_2_s0;

  Half_Adder half_adder_1 (.x(carry), .y(half_adder_2_s0), .s0(s0), .Carry_Out(half_adder_1_carry_out));
  Half_Adder half_adder_2 (.x(x), .y(y), .s0(half_adder_2_s0), .Carry_Out(half_adder_2_carry_out));
  or or_1 (Carry_out, half_adder_1_carry_out, half_adder_2_carry_out);
endmodule

module Somador_3_Bits (
  input  op,
  input  a0,
  input  b0,
  input  a1,
  input  b1,
  input  a2,
  input  b2,
  output out_8,
  output out_9,
  output out_10,
  output out_11
);

  wire full_adder_1_carry_out, full_adder_2_carry_out;

  Full_Adder full_adder_1 (.carry(op), .x(a0), .y(b0), .s0(out_8), .Carry_out(full_adder_1_carry_out));
  Full_Adder full_adder_2 (
    .carry(full_adder_1_carry_out), .x(a1), .y(b1), .s0(out_9), .Carry_out(full_adder_2_carry_out));
  Full_Adder full_adder_3 (.carry(full_adder_2_carry_out), .x(a2), .y(b2), .s0(out_10), .Carry_out(out_11));
endmodule
