// Logisim project Subtrator 2 bits.circ as structural Verilog
module Half_Subtractor (
  input  x,
  input  y,
  output s0,
  output s1
);

  wire not_1_out;

  xor xor_1 (s0, x, y);
  not not_1 (not_1_out, x);
  and and_1 (s1, not_1_out, y);
endmodule

module Full_Sub (
  input  Carry_in,
  input  x,
  input  y,
  output s0,
  output Carry_Out
);

  wire half_subtractor_1_s0, half_subtractor_1_s1, half_subtractor_2_s1;

  Half_Subtractor half_subtractor_1 (.x(x), .y(y), .s0(half_subtractor_1_s0), .s1(half_subtractor_1_s1));
  Half_Subtractor half_subtractor_2 (.x(half_subtractor_1_s0), .y(Carry_in), .s0(s0), .s1(half_subtractor_2_s1));
  or or_1 (Carry_Out, half_subtractor_2_s1, half_subtractor_1_s1);
endmodule

module Sub_2_bits (
  input  Carry_In,
  input  a0,
  input  b0,
  input  a1,
  input  b1,
  output s0,
  output s1,
  output Carry_out
);

  wire full_sub_1_carry_out;

  Full_Sub full_sub_1 (.Carry_in(Carry_In), .x(a0), .y(b0), .s0(s0), .Carry_Out(full_sub_1_carry_out));
  Full_Sub full_sub_2 (.Carry_in(full_sub_1_carry_out), .x(a1), .y(b1), .s0(s1), .Carry_Out(Carry_out));
endmodule
