// Logisim project guia_05.circ as structural Verilog: 7 circuits, main circuit ex01
module ex01 (
  input  x0,
  input  x1,
  input  x2,
  input  y0,
  input  y1,
  input  y2,
  output s0,
  output s1,
  output s2,
  output s4
);

  wire full_adder_1_s1, half_adder_1_s1;

  half_adder half_adder_1 (.x(x0), .y(y0), .s0(s0), .s1(half_adder_1_s1));
  full_adder full_adder_1 (.v_in(half_adder_1_s1), .x(x1), .y(y1), .s0(s1), .s1(full_adder_1_s1));
  full_adder full_adder_2 (.v_in(full_adder_1_s1), .x(x2), .y(y2), .s0(s2), .s1(s4));

  // Notes on the sheet:
  //   Não considerando sinal
endmodule

module half_adder (
  input  x,
  input  y,
  output s0,
  output s1
);

  xor xor_1 (s0, x, y);
  and and_1 (s1, x, y);
endmodule

module full_adder (
  input  v_in,
  input  x,
  input  y,
  output s0,
  output s1
);

  wire half_adder_1_s0, half_adder_1_s1, half_adder_2_s1;

  half_adder half_adder_1 (.x(x), .y(y), .s0(half_adder_1_s0), .s1(half_adder_1_s1));
  half_adder half_adder_2 (.x(v_in), .y(half_adder_1_s0), .s0(s0), .s1(half_adder_2_s1));
  or or_1 (s1, half_adder_2_s1, half_adder_1_s1);
endmodule

module half_sub (
  input  y,
  input  x,
  output s0,
  output b_out
);

  wire not_1_out;

  not not_1 (not_1_out, x);
  xor xor_1 (s0, y, x);
  and and_1 (b_out, not_1_out, y);
endmodule

module full_sub (
  input  borrow_in,
  input  y,
  input  x,
  output s0,
  output s1
);

  wire half_sub_1_b_out, half_sub_1_s0, half_sub_2_b_out;

  half_sub half_sub_1 (.y(y), .x(x), .s0(half_sub_1_s0), .b_out(half_sub_1_b_out));
  half_sub half_sub_2 (.y(borrow_in), .x(half_sub_1_s0), .s0(s0), .b_out(half_sub_2_b_out));
  or or_1 (s1, half_sub_2_b_out, half_sub_1_b_out);
endmodule

module ex02 (
  input  x0,
  input  x1,
  input  y0,
  input  y1,
  output s1,
  output s2,
  output s3
);

  wire half_sub_1_b_out;

  half_sub half_sub_1 (.y(y0), .x(x0), .s0(s1), .b_out(half_sub_1_b_out));
  full_sub full_sub_1 (.borrow_in(half_sub_1_b_out), .y(y1), .x(x1), .s0(s2), .s1(s3));
endmodule

module ex03 (
  input  x0,
  input  x1,
  input  y0,
  input  y1,
  output s0,
  output s1,
  output s2,
  output s3
);

  wire and_2_out, and_3_out, and_4_out, ex01_1_s1;

  and and_1 (s0, x0, y0);
  and and_2 (and_2_out, x1, y0);
  and and_3 (and_3_out, x0, y1);
  and and_4 (and_4_out, x1, y1);
  ex01 ex01_1 (.x0(and_2_out), .y0(and_3_out), .s0(s1), .s1(ex01_1_s1));  // open: x1, x2, y1, y2, s2, s4
  ex01 ex01_2 (.x0(ex01_1_s1), .y0(and_4_out), .s0(s2), .s1(s3));  // open: x1, x2, y1, y2, s2, s4

  // Notes on the sheet:
  //   Não considerando sinal
endmodule
