// Logisim project Guia05_01.circ as structural Verilog: 3 circuits, main circuit Full_Adder
module Full_Adder (
  input  [2:0] Cin,
  input  [2:0] X,
  input  [2:0] Y,
  output [2:0] Cout,
  output [2:0] s1
);

  wire [2:0] half_adder2_1_s1, half_adder_1_s0, half_adder_1_s1;

  Half_Adder half_adder_1 (.X(X), .Y(Y), .s0(half_adder_1_s0), .s1(half_adder_1_s1));
  Half_Adder2 half_adder2_1 (.X(Cin), .Y(half_adder_1_s0), .s0(Cout), .s1(half_adder2_1_s1));
  assign s1 = half_adder2_1_s1 | half_adder_1_s1;  // OR_Gate or_1, 3 bits wide
endmodule

module Half_Adder (
  input  [2:0] X,
  input  [2:0] Y,
  output [2:0] s0,
  output [2:0] s1
);

  assign s0 = X ^ Y;  // XOR_Gate xor_1, 3 bits wide
  assign s1 = X & Y;  // AND_Gate and_1, 3 bits wide
endmodule

module Half_Adder2 (
  input  [2:0] X,
  input  [2:0] Y,
  output [2:0] s0,
  output [2:0] s1
);

  assign s0 = X ^ Y;  // XOR_Gate xor_1, 3 bits wide
  assign s1 = X & Y;  // AND_Gate and_1, 3 bits wide
endmodule
