// Logisim project Guia05_03.circ as structural Verilog: 3 circuits, main circuit Multiplicador
module Multiplicador (
  input  b1,
  input  b0,
  input  b1_2,
  input  b0_2,
  input  a0,
  input  a1,
  output m3,
  output m2,
  output m1,
  output m0
);

  wire and_1_out, and_2_out, and_3_out, half_adder2_1_cout;

  and and_1 (and_1_out, a1, b1);
  Half_Adder half_adder_1 (.X(half_adder2_1_cout), .Y(and_1_out), .s0(m2), .Cout(m3));
  and and_2 (and_2_out, a1, b0);
  and and_3 (and_3_out, a0, b1_2);
  Half_Adder2 half_adder2_1 (.X(and_3_out), .Y(and_2_out), .s0(m1), .Cout(half_adder2_1_cout));
  and and_4 (m0, a0, b0_2);
endmodule

module Half_Adder (
  input  X,
  input  Y,
  output s0,
  output Cout
);

  xor xor_1 (s0, X, Y);
  and and_1 (Cout, X, Y);
endmodule

module Half_Adder2 (
  input  X,
  input  Y,
  output s0,
  output Cout
);

  xor xor_1 (s0, X, Y);
  and and_1 (Cout, X, Y);
endmodule
