// Logisim project Guia05_04.circ as structural Verilog: 3 circuits, main circuit main
module main (
  input  B2,
  input  B1,
  input  B0,
  input  A2,
  input  A1,
  input  A0,
  output S3,
  output S2,
  output S1,
  output S0
);

  wire full_adder_1_cout, full_adder_3_cout;

  Full_Adder full_adder_1 (.B(A1), .A(B1), .Cin(full_adder_3_cout), .Cout(full_adder_1_cout), .S(S1));
  Full_Adder full_adder_2 (.B(B2), .A(A2), .Cin(full_adder_1_cout), .Cout(S3), .S(S2));
  Full_Adder full_adder_3 (.B(B0), .A(A0), .Cin(1'b0), .Cout(full_adder_3_cout), .S(S0));
endmodule

module Half_Adder (
  input  B,
  input  A,
  output Cout,
  output S
);

  wire nand_1_out, nand_2_out, nand_3_out, nand_4_out, nand_5_out;

  nand nand_1 (nand_1_out, A, A);
  nand nand_2 (nand_2_out, B, B);
  nand nand_3 (nand_3_out, A, B);
  nand nand_4 (nand_4_out, B, nand_1_out);
  nand nand_5 (nand_5_out, nand_2_out, A);
  nand nand_6 (Cout, nand_3_out, nand_3_out);
  nand nand_7 (S, nand_4_out, nand_5_out);
endmodule

module Full_Adder (
  input  B,
  input  A,
  input  Cin,
  output Cout,
  output S
);

  wire half_adder_1_cout, half_adder_1_s, half_adder_2_cout, nand_1_out, nand_2_out;

  Half_Adder half_adder_1 (.B(B), .A(A), .Cout(half_adder_1_cout), .S(half_adder_1_s));
  Half_Adder half_adder_2 (.B(half_adder_1_s), .A(Cin), .Cout(half_adder_2_cout), .S(S));
  nand nand_1 (nand_1_out, half_adder_2_cout, half_adder_2_cout);
  nand nand_2 (nand_2_out, half_adder_1_cout, half_adder_1_cout);
  nand nand_3 (Cout, nand_1_out, nand_2_out);
endmodule
