// Logisim project exercicio01.circ as structural Verilog
module meiasoma (
  input  a,
  input  b,
  output s0,
  output s1
);

  xor xor_1 (s0, a, b);
  and and_1 (s1, a, b);
endmodule

module somacompleta (
  input  c,
  input  a,
  input  b,
  output s0,
  output s1
);

  wire meiasoma_1_s0, meiasoma_1_s1, meiasoma_2_s1;

  meiasoma meiasoma_1 (.a(a), .b(b), .s0(meiasoma_1_s0), .s1(meiasoma_1_s1));
  meiasoma meiasoma_2 (.a(c), .b(meiasoma_1_s0), .s0(s0), .s1(meiasoma_2_s1));
  or or_1 (s1, meiasoma_2_s1, meiasoma_1_s1);
endmodule

module somacompleta3bits (
  input  a0,
  input  a1,
  input  a2,
  input  b0,
  input  b1,
  input  b2,
  output s0,
  output s1,
  output s2,
  output s3
);

  wire meiasoma_1_s1, somacompleta_1_s1;

  meiasoma meiasoma_1 (.a(a0), .b(b0), .s0(s0), .s1(meiasoma_1_s1));
  somacompleta somacompleta_1 (.c(meiasoma_1_s1), .a(a1), .b(b1), .s0(s1), .s1(somacompleta_1_s1));
  somacompleta somacompleta_2 (.c(somacompleta_1_s1), .a(a2), .b(b2), .s0(s2), .s1(s3));
endmodule
