// Logisim project diagramas do logisim.circ as structural Verilog: 10 circuits, main circuit meia_soma
module meia_soma (
  input  A,
  input  B,
  output S0,
  output S1
);

  xor xor_1 (S0, A, B);
  and and_1 (S1, A, B);
endmodule

module soma_completa_1bit (
  input  A,
  input  B,
  input  C,
  output S0,
  output S1
);

  wire meia_soma_1_s0, meia_soma_1_s1, meia_soma_2_s1;

  meia_soma meia_soma_1 (.A(A), .B(B), .S0(meia_soma_1_s0), .S1(meia_soma_1_s1));
  meia_soma meia_soma_2 (.A(meia_soma_1_s0), .B(C), .S0(S0), .S1(meia_soma_2_s1));
  or or_1 (S1, meia_soma_2_s1, meia_soma_1_s1);

  // Notes on the sheet:
  //   meia-soma
  //   meia-soma
endmodule

module soma_completa_3bits (
  input  a2,
  input  a1,
  input  a0,
  input  b2,
  input  b1,
  input  b0,
  output s3,
  output s2,
  output s1,
  output s0
);

  wire soma_completa_1bit_1_s1, soma_completa_1bit_2_s1;

  soma_completa_1bit soma_completa_1bit_1 (.A(a0), .B(b0), .C(1'b0), .S0(s0), .S1(soma_completa_1bit_1_s1));
  soma_completa_1bit soma_completa_1bit_2 (
    .A(a1), .B(b1), .C(soma_completa_1bit_1_s1), .S0(s1), .S1(soma_completa_1bit_2_s1));
  soma_completa_1bit soma_completa_1bit_3 (.A(a2), .B(b2), .C(soma_completa_1bit_2_s1), .S0(s2), .S1(s3));

  // Notes on the sheet:
  //   A + B
  //   soma_completa_1bit
  //   soma_completa_1bit
  //   soma_completa_1bit
endmodule

module \meia_diferença  (
  input  A,
  input  B,
  output S0,
  output S1
);

  wire and_1_out, and_2_out, not_1_out, not_2_out, not_3_out;

  not not_1 (not_1_out, A);
  not not_2 (not_2_out, B);
  not not_3 (not_3_out, A);
  and and_1 (and_1_out, not_1_out, B);
  and and_2 (and_2_out, A, not_2_out);
  and and_3 (S1, not_3_out, B);
  or or_1 (S0, and_1_out, and_2_out);
endmodule

module \diferença_completa_1bit  (
  input  A,
  input  B,
  input  C,
  output S0,
  output S1
);

  wire \meia_diferença_1_s0 , \meia_diferença_1_s1 , \meia_diferença_2_s1 ;

  \meia_diferença  \meia_diferença_1  (.A(A), .B(B), .S0(\meia_diferença_1_s0 ), .S1(\meia_diferença_1_s1 ));
  \meia_diferença  \meia_diferença_2  (.A(\meia_diferença_1_s0 ), .B(C), .S0(S0), .S1(\meia_diferença_2_s1 ));
  or or_1 (S1, \meia_diferença_2_s1 , \meia_diferença_1_s1 );

  // Notes on the sheet:
  //   meia-diferença
  //   meia-diferença
endmodule

module \diferença_completa_2bits  (
  input  a1,
  input  a0,
  input  b1,
  input  b0,
  output s2,
  output s1,
  output s0
);

  wire \diferença_completa_1bit_1_s1 ;

  \diferença_completa_1bit  \diferença_completa_1bit_1  (
    .A(a0), .B(b0), .C(1'b0), .S0(s0), .S1(\diferença_completa_1bit_1_s1 ));
  \diferença_completa_1bit  \diferença_completa_1bit_2  (
    .A(a1), .B(b1), .C(\diferença_completa_1bit_1_s1 ), .S0(s1), .S1(s2));

  // Notes on the sheet:
  //   A - B
  //   diferença_completa_1bit
  //   diferença_completa_1bit
endmodule

module multiplicador_2bits (
  input  a1,
  input  a0,
  input  b1,
  input  b0,
  output s3,
  output s2,
  output s1,
  output s0
);

  wire and_2_out, and_3_out, and_4_out, meia_soma_1_s1;

  and and_1 (s0, a0, b0);
  and and_2 (and_2_out, a0, b1);
  and and_3 (and_3_out, a1, b0);
  and and_4 (and_4_out, a1, b1);
  meia_soma meia_soma_1 (.A(and_2_out), .B(and_3_out), .S0(s1), .S1(meia_soma_1_s1));
  soma_completa_1bit soma_completa_1bit_1 (.A(and_4_out), .B(1'b0), .C(meia_soma_1_s1), .S0(s2), .S1(s3));

  // Notes on the sheet:
  //   A x B
  //   meia_soma
  //   soma_completa_1bit
endmodule

module \meia_diferença_nor  (
  input  a,
  input  b,
  output s0,
  output s1
);

  wire nor_1_out, nor_2_out, nor_3_out, nor_4_out, nor_5_out, nor_6_out, nor_7_out;

  nor nor_1 (nor_1_out, a, a);
  nor nor_2 (nor_2_out, b, b);
  nor nor_3 (nor_3_out, a, b);
  nor nor_4 (nor_4_out, a, a);
  nor nor_5 (nor_5_out, nor_1_out, nor_2_out);
  nor nor_6 (nor_6_out, nor_4_out, nor_4_out);
  nor nor_7 (nor_7_out, b, b);
  nor nor_8 (s0, nor_5_out, nor_3_out);
  nor nor_9 (s1, nor_6_out, nor_7_out);

  // Notes on the sheet:
  //   3
endmodule

module \diferença_completa_1bit_nor  (
  input  a,
  input  b,
  input  c,
  output s0,
  output s1
);

  wire \meia_diferença_nor_1_s0 , \meia_diferença_nor_1_s1 , \meia_diferença_nor_2_s1 ;

  \meia_diferença_nor  \meia_diferença_nor_1  (
    .a(a), .b(b), .s0(\meia_diferença_nor_1_s0 ), .s1(\meia_diferença_nor_1_s1 ));
  \meia_diferença_nor  \meia_diferença_nor_2  (
    .a(\meia_diferença_nor_1_s0 ), .b(c), .s0(s0), .s1(\meia_diferença_nor_2_s1 ));
  or or_1 (s1, \meia_diferença_nor_2_s1 , \meia_diferença_nor_1_s1 );

  // Notes on the sheet:
  //   meia_diferença_nor
  //   meia_diferença_nor
endmodule

module \diferença_completa_2bits_nor  (
  input  a1,
  input  a0,
  input  b1,
  input  b0,
  output s2,
  output s1,
  output s0
);

  wire \diferença_completa_1bit_nor_1_s1 ;

  \diferença_completa_1bit_nor  \diferença_completa_1bit_nor_1  (
    .a(a0), .b(b0), .c(1'b0), .s0(s0), .s1(\diferença_completa_1bit_nor_1_s1 ));
  \diferença_completa_1bit_nor  \diferença_completa_1bit_nor_2  (
    .a(a1), .b(b1), .c(\diferença_completa_1bit_nor_1_s1 ), .s0(s1), .s1(s2));

  // Notes on the sheet:
  //   diferença_completa_1bit_nor
  //   diferença_completa_1bit_nor
endmodule
