// Logisim project exercicio01.circ as structural Verilog: 3 circuits, main circuit main
module main (
  input  [2:0] a,
  input  [2:0] b,
  output [3:0] Retultado
);

  wire full_adder_1_vai_um, half_adder_1_vai_um;

  half_adder half_adder_1 (.a(a[0]), .b(b[0]), .Resto(Retultado[0]), .Vai_um(half_adder_1_vai_um));
  full_adder full_adder_1 (
    .Vem_um(half_adder_1_vai_um), .a(a[1]), .b(b[1]), .Resto(Retultado[1]), .Vai_um(full_adder_1_vai_um));
  full_adder full_adder_2 (
    .Vem_um(full_adder_1_vai_um), .a(a[2]), .b(b[2]), .Resto(Retultado[2]), .Vai_um(Retultado[3]));

  // Notes on the sheet:
  //   Guia_05 - Exercicio01
  //   Circuito de Soma Completa com 3  bits
  //   Autor: Tiago Menegaz de Melo Garcia
  //   Matrícula: 405844
endmodule

module half_adder (
  input  a,
  input  b,
  output Resto,
  output Vai_um
);

  xor xor_1 (Resto, a, b);
  and and_1 (Vai_um, b, a);
endmodule

module full_adder (
  input  Vem_um,
  input  a,
  input  b,
  output Resto,
  output Vai_um
);

  wire and_1_out, and_2_out, xor_1_out;

  xor xor_1 (xor_1_out, a, b);
  and and_1 (and_1_out, b, a);
  xor xor_2 (Resto, Vem_um, xor_1_out);
  and and_2 (and_2_out, Vem_um, xor_1_out);
  or or_1 (Vai_um, and_2_out, and_1_out);
endmodule
