// Logisim project exercicio02.circ as structural Verilog: 3 circuits, main circuit main
module main (
  input  [2:0] a,
  input  [2:0] b,
  output [3:0] Retultado
);

  wire full_subtractor_1_vem_um_2, half_subtractor_1_vem_um;

  half_subtractor half_subtractor_1 (.a(a[0]), .b(b[0]), .Resto(Retultado[0]), .Vem_um(half_subtractor_1_vem_um));
  full_subtractor full_subtractor_1 (
    .Vem_um(half_subtractor_1_vem_um), .a(a[1]), .b(b[1]), .Resto(Retultado[1]),
    .Vem_um_2(full_subtractor_1_vem_um_2));
  full_subtractor full_subtractor_2 (
    .Vem_um(full_subtractor_1_vem_um_2), .a(a[2]), .b(b[2]), .Resto(Retultado[2]), .Vem_um_2(Retultado[3]));

  // Notes on the sheet:
  //   Guia_05 - Exercicio02
  //   Circuito de Subtração Completa com 3 btis
  //   Autor: Tiago Menegaz de Melo Garcia
  //   Matrícula: 405844
endmodule

module half_subtractor (
  input  a,
  input  b,
  output Resto,
  output Vem_um
);

  wire not_1_out;

  xor xor_1 (Resto, a, b);
  not not_1 (not_1_out, a);
  and and_1 (Vem_um, not_1_out, b);
endmodule

module full_subtractor (
  input  Vem_um,
  input  a,
  input  b,
  output Resto,
  output Vem_um_2
);

  wire and_1_out, and_2_out, not_1_out, not_2_out, xor_1_out;

  not not_1 (not_1_out, a);
  xor xor_1 (xor_1_out, a, b);
  and and_1 (and_1_out, b, not_1_out);
  not not_2 (not_2_out, xor_1_out);
  xor xor_2 (Resto, Vem_um, xor_1_out);
  and and_2 (and_2_out, Vem_um, not_2_out);
  or or_1 (Vem_um_2, and_2_out, and_1_out);
endmodule
