// Logisim project exercicio03.circ as structural Verilog: 3 circuits, main circuit main
module main (
  input  [1:0] b,
  input  [1:0] a,
  output [3:0] Resto
);

  wire and_2_out, and_3_out, and_4_out, half_adder_1_vai_um;

  and and_1 (Resto[0], a[0], b[0]);
  and and_2 (and_2_out, a[0], b[1]);
  and and_3 (and_3_out, b[0], a[1]);
  and and_4 (and_4_out, a[1], b[1]);
  half_adder half_adder_1 (.a(and_2_out), .b(and_3_out), .Resto(Resto[1]), .Vai_um(half_adder_1_vai_um));
  full_adder full_adder_1 (.Vem_um(half_adder_1_vai_um), .a(1'b0), .b(and_4_out), .Resto(Resto[2]), .Vai_um(Resto[3]));

  // Notes on the sheet:
  //   Guia_05 - Exercicio03
  //   Matrícula: 405844
  //   Circuito de Produto Completo
  //   Autor: Tiago Menegaz de Melo Garcia
endmodule

module half_adder (
  input  a,
  input  b,
  output Resto,
  output Vai_um
);

  xor xor_1 (Resto, a, b);
  and and_1 (Vai_um, b, a);
endmodule

module full_adder (
  input  Vem_um,
  input  a,
  input  b,
  output Resto,
  output Vai_um
);

  wire and_1_out, and_2_out, xor_1_out;

  xor xor_1 (xor_1_out, b, a);
  and and_1 (and_1_out, a, b);
  xor xor_2 (Resto, xor_1_out, Vem_um);
  and and_2 (and_2_out, Vem_um, xor_1_out);
  or or_1 (Vai_um, and_2_out, and_1_out);
endmodule
