// Logisim project exercicio04.circ as structural Verilog: 5 circuits, main circuit main
module main (
  input  [1:0] a,
  input  [1:0] b,
  output [2:0] Resultado
);

  wire half_adder_nand_only_1_vai_um;

  half_adder_NAND_only half_adder_nand_only_1 (
    .a(a[0]), .b(b[0]), .Resto(Resultado[0]), .Vai_um(half_adder_nand_only_1_vai_um));
  full_adder_NAND_only full_adder_nand_only_1 (
    .Vem_um(half_adder_nand_only_1_vai_um), .a(a[1]), .b(b[1]), .Resto(Resultado[1]), .Vai_um(Resultado[2]));

  // Notes on the sheet:
  //   Guia_05 - Exercicio04
  //   Circuito de Soma Completa com apenas portas NAND
  //   Autor: Tiago Menegaz de Melo Garcia
  //   Matrícula: 405844
endmodule

module half_adder_NAND_only (
  input  a,
  input  b,
  output Resto,
  output Vai_um
);

  wire nand_1_out;

  XOR_with_NAND xor_with_nand_1 (.a(a), .b(b), .out_3(Resto));
  nand nand_1 (nand_1_out, a, b);
  nand nand_2 (Vai_um, nand_1_out, nand_1_out);
endmodule

module XOR_with_NAND (
  input  a,
  input  b,
  output out_3
);

  wire nand_1_out, nand_2_out, nand_3_out, nand_4_out, nand_5_out;

  nand nand_1 (nand_1_out, a, a);
  nand nand_2 (nand_2_out, b, b);
  nand nand_3 (nand_3_out, a, b);
  nand nand_4 (nand_4_out, nand_1_out, nand_2_out);
  nand nand_5 (nand_5_out, nand_3_out, nand_4_out);
  nand nand_6 (out_3, nand_5_out, nand_5_out);
endmodule

module full_adder_NAND_only (
  input  Vem_um,
  input  a,
  input  b,
  output Resto,
  output Vai_um
);

  wire nand_1_out, nand_2_out, nand_3_out, nand_4_out, xor_with_nand_1_out_3;

  XOR_with_NAND xor_with_nand_1 (.a(a), .b(b), .out_3(xor_with_nand_1_out_3));
  nand nand_1 (nand_1_out, b, a);
  XOR_with_NAND xor_with_nand_2 (.a(Vem_um), .b(xor_with_nand_1_out_3), .out_3(Resto));
  nand nand_2 (nand_2_out, Vem_um, xor_with_nand_1_out_3);
  nand nand_3 (nand_3_out, nand_1_out, nand_1_out);
  nand nand_4 (nand_4_out, nand_2_out, nand_2_out);
  OR_with_NAND or_with_nand_1 (.a(nand_4_out), .b(nand_3_out), .out_3(Vai_um));
endmodule

module OR_with_NAND (
  input  a,
  input  b,
  output out_3
);

  wire nand_1_out, nand_2_out;

  nand nand_1 (nand_1_out, a, a);
  nand nand_2 (nand_2_out, b, b);
  nand nand_3 (out_3, nand_1_out, nand_2_out);
endmodule
