// Logisim project exercicio05.circ as structural Verilog: 6 circuits, main circuit main
module main (
  input  [1:0] a,
  input  [1:0] b,
  output [2:0] Resto
);

  wire half_subtractor_1_vem_um;

  half_subtractor half_subtractor_1 (.a(a[0]), .b(b[0]), .Resto(Resto[0]), .Vem_um(half_subtractor_1_vem_um));
  full_subtractor full_subtractor_1 (
    .Veum_um(half_subtractor_1_vem_um), .a(a[1]), .b(b[1]), .Resto(Resto[1]), .Vem_um(Resto[2]));

  // Notes on the sheet:
  //   Guia_05 - Exercicio05
  //   Circuito de Subtração completa com NOR
  //   Autor: Tiago Menegaz de Melo Garcia
  //   Matrícula: 405844
endmodule

module XOR_with_NOR (
  input  a,
  input  b,
  output s
);

  wire nor_1_out, nor_2_out, nor_3_out, nor_4_out;

  nor nor_1 (nor_1_out, a, b);
  nor nor_2 (nor_2_out, b, b);
  nor nor_3 (nor_3_out, a, a);
  nor nor_4 (nor_4_out, nor_2_out, nor_3_out);
  nor nor_5 (s, nor_1_out, nor_4_out);
endmodule

module AND_with_NOR (
  input  a,
  input  b,
  output s
);

  wire nor_1_out, nor_2_out;

  nor nor_1 (nor_1_out, a, a);
  nor nor_2 (nor_2_out, b, b);
  nor nor_3 (s, nor_1_out, nor_2_out);
endmodule

module half_subtractor (
  input  a,
  input  b,
  output Resto,
  output Vem_um
);

  wire nor_1_out;

  XOR_with_NOR xor_with_nor_1 (.a(a), .b(b), .s(Resto));
  nor nor_1 (nor_1_out, a, a);
  AND_with_NOR and_with_nor_1 (.a(nor_1_out), .b(b), .s(Vem_um));
endmodule

module full_subtractor (
  input  Veum_um,
  input  a,
  input  b,
  output Resto,
  output Vem_um
);

  wire and_with_nor_1_s, and_with_nor_2_s, nor_1_out, nor_2_out, xor_with_nor_1_s;

  XOR_with_NOR xor_with_nor_1 (.a(a), .b(b), .s(xor_with_nor_1_s));
  AND_with_NOR and_with_nor_1 (.a(b), .b(nor_1_out), .s(and_with_nor_1_s));
  nor nor_1 (nor_1_out, b, a);
  XOR_with_NOR xor_with_nor_2 (.a(Veum_um), .b(xor_with_nor_1_s), .s(Resto));
  AND_with_NOR and_with_nor_2 (.a(Veum_um), .b(nor_2_out), .s(and_with_nor_2_s));
  not nor_2 (nor_2_out, xor_with_nor_1_s);  // NOR_Gate
  OR_with_NOR or_with_nor_1 (.a(and_with_nor_2_s), .b(and_with_nor_1_s), .S(Vem_um));
endmodule

module OR_with_NOR (
  input  a,
  input  b,
  output S
);

  wire nor_1_out;

  nor nor_1 (nor_1_out, a, b);
  nor nor_2 (S, nor_1_out, nor_1_out);
endmodule
