// Logisim project circ01.circ as structural Verilog: 3 circuits, main circuit main
module main (
  input  CARRY,
  input  A,
  input  B,
  output S0,
  output S1
);

  wire meiasoma_1_s0, meiasoma_1_s1, meiasoma_2_s1;

  meiasoma meiasoma_1 (.A(A), .B(B), .S0(meiasoma_1_s0), .S1(meiasoma_1_s1));
  meiasoma meiasoma_2 (.A(CARRY), .B(meiasoma_1_s0), .S0(S0), .S1(meiasoma_2_s1));
  or or_1 (S1, meiasoma_2_s1, meiasoma_1_s1);
endmodule

module meiasoma (
  input  A,
  input  B,
  output S0,
  output S1
);

  xor xor_1 (S0, A, B);
  and and_1 (S1, B, A);
endmodule

module somacompleta (
  input  a0,
  input  b0,
  input  a1,
  input  b1,
  input  a2,
  input  b2,
  output s0,
  output s1,
  output s2,
  output s3
);

  wire main_1_s1, meiasoma_1_s1;

  meiasoma meiasoma_1 (.A(a0), .B(b0), .S0(s0), .S1(meiasoma_1_s1));
  main main_1 (.CARRY(meiasoma_1_s1), .A(a1), .B(b1), .S0(s1), .S1(main_1_s1));
  main main_2 (.CARRY(main_1_s1), .A(a2), .B(b2), .S0(s2), .S1(s3));

  // Notes on the sheet:
  //   Soma 3 bits
endmodule
