// Logisim project circ03.circ as structural Verilog: 2 circuits, main circuit main
module main (
  input  a,
  input  b,
  output s0,
  output s1
);

  xor xor_1 (s0, a, b);
  and and_1 (s1, b, a);
endmodule

module meiasoma (
  input  a0,
  input  b0,
  input  a1,
  input  b1,
  output s0,
  output s1,
  output s2,
  output s3
);

  wire and_2_out, and_3_out, and_4_out, main_1_s1;

  and and_1 (s0, a0, b0);
  and and_2 (and_2_out, b0, a1);
  and and_3 (and_3_out, a0, b1);
  and and_4 (and_4_out, a1, b1);
  main main_1 (.a(and_2_out), .b(and_3_out), .s0(s1), .s1(main_1_s1));
  main main_2 (.a(main_1_s1), .b(and_4_out), .s0(s2), .s1(s3));

  // Notes on the sheet:
  //   Produto
endmodule
