// Logisim project guia5 - 412727.circ as structural Verilog: 12 circuits, main circuit main
module main (
  input  A0,
  input  A1,
  input  A2,
  input  B0,
  input  B1,
  input  B2,
  input  C,
  output [3:0] EX1,
  output [2:0] EX2,
  output [3:0] EX3,
  output [2:0] out_11,
  output [2:0] EX5
);

  ex2 ex2_1 (.a0(A0), .b0(B0), .a1(A1), .b1(B1), .S0(EX2[0]), .S1(EX2[1]), .S2(EX2[2]));
  ex3 ex3_1 (.a1(A1), .b1(B1), .a0(A0), .b0(B1), .out_5(EX3[3]), .out_6(EX3[2]), .out_7(EX3[1]), .out_8(EX3[0]));
  ex4 ex4_1 (.A0(A0), .B0(B0), .C(C), .A1(A1), .B1(B1), .S0(out_11[0]), .S1(out_11[1]), .S2(out_11[2]));
  ex5 ex5_1 (.A0(A0), .B0(B0), .C(C), .A1(A1), .B1(B1), .S0(EX5[0]), .S1(EX5[1]), .S2(EX5[2]));
  ex1 ex1_1 (.a({A2, A1, A0}), .b({B2, B1, B0}), .s(EX1));

  // Notes on the sheet:
  //   AUGUSTO FERREIRA ANDRADE DO CARMO - 412727 - GUIA 5
  //   EX3
  //   EX4
endmodule

module Meia_soma__nand (
  input  A,
  input  B,
  output s0,
  output s1
);

  wire nand_1_out, nand_2_out, nand_3_out, nand_4_out, nand_5_out;

  nand nand_1 (nand_1_out, A, A);
  nand nand_2 (nand_2_out, B, B);
  nand nand_3 (nand_3_out, A, B);
  nand nand_4 (nand_4_out, nand_1_out, B);
  nand nand_5 (nand_5_out, nand_2_out, A);
  nand nand_6 (s1, nand_3_out, nand_3_out);
  nand nand_7 (s0, nand_4_out, nand_5_out);
endmodule

module Soma_Completa__meia_soma (
  input  A,
  input  B,
  input  C,
  output S0,
  output S1
);

  wire meia_soma_nand_1_s0, meia_soma_nand_1_s1, meia_soma_nand_2_s1;

  Meia_soma__nand meia_soma_nand_1 (.A(A), .B(B), .s0(meia_soma_nand_1_s0), .s1(meia_soma_nand_1_s1));
  Meia_soma__nand meia_soma_nand_2 (.A(meia_soma_nand_1_s0), .B(C), .s0(S0), .s1(meia_soma_nand_2_s1));
  or or_1 (S1, meia_soma_nand_2_s1, meia_soma_nand_1_s1);
endmodule

module \Meia_Diferença  (
  input  A,
  input  B,
  output S0,
  output S1
);

  wire not_1_out;

  not not_1 (not_1_out, A);
  xor xor_1 (S0, A, B);
  and and_1 (S1, B, not_1_out);
endmodule

module \Diferença_completa__meia_diferença  (
  input  A,
  input  B,
  input  C,
  output S0,
  output S1
);

  wire \meia_diferença_1_s0 , \meia_diferença_1_s1 , \meia_diferença_2_s1 ;

  \Meia_Diferença  \meia_diferença_1  (.A(A), .B(B), .S0(\meia_diferença_1_s0 ), .S1(\meia_diferença_1_s1 ));
  \Meia_Diferença  \meia_diferença_2  (.A(\meia_diferença_1_s0 ), .B(C), .S0(S0), .S1(\meia_diferença_2_s1 ));
  or or_1 (S1, \meia_diferença_2_s1 , \meia_diferença_1_s1 );
endmodule

module \meia_diferença__nor  (
  input  A,
  input  B,
  output s0,
  output s1
);

  wire nor_1_out, nor_2_out, nor_3_out, nor_4_out, nor_6_out;

  nor nor_1 (nor_1_out, A, A);
  nor nor_2 (nor_2_out, B, B);
  nor nor_3 (nor_3_out, nor_1_out, B);
  nor nor_4 (nor_4_out, nor_2_out, A);
  nor nor_5 (s1, nor_2_out, A);
  nor nor_6 (nor_6_out, nor_3_out, nor_4_out);
  nor nor_7 (s0, nor_6_out, nor_6_out);
endmodule

module ex1 (
  input  [2:0] a,
  input  [2:0] b,
  output [3:0] s
);

  wire meia_soma_nand_1_s1, soma_completa_meia_soma_1_s1;

  Meia_soma__nand meia_soma_nand_1 (.A(a[0]), .B(b[0]), .s0(s[0]), .s1(meia_soma_nand_1_s1));
  Soma_Completa__meia_soma soma_completa_meia_soma_1 (
    .A(a[1]), .B(b[1]), .C(meia_soma_nand_1_s1), .S0(s[1]), .S1(soma_completa_meia_soma_1_s1));
  Soma_Completa__meia_soma soma_completa_meia_soma_2 (
    .A(a[2]), .B(b[2]), .C(soma_completa_meia_soma_1_s1), .S0(s[2]), .S1(s[3]));
endmodule

module ex2 (
  input  a0,
  input  b0,
  input  a1,
  input  b1,
  output S0,
  output S1,
  output S2
);

  wire \meia_diferença_nor_1_s1 ;

  \meia_diferença__nor  \meia_diferença_nor_1  (.A(a0), .B(b0), .s0(S0), .s1(\meia_diferença_nor_1_s1 ));
  \diferença_completa_normal  \diferença_completa_normal_1  (
    .in_1(a1), .in_2(b1), .in_3(\meia_diferença_nor_1_s1 ), .out_4(S1), .out_5(S2));
endmodule

module \diferença_completa_normal  (
  input  in_1,
  input  in_2,
  input  in_3,
  output out_4,
  output out_5
);

  wire and_1_out, and_2_out, not_1_out, not_2_out, xor_1_out;

  not not_1 (not_1_out, in_1);
  xor xor_1 (xor_1_out, in_1, in_2);
  and and_1 (and_1_out, in_2, not_1_out);
  not not_2 (not_2_out, xor_1_out);
  xor xor_2 (out_4, in_3, xor_1_out);
  and and_2 (and_2_out, not_2_out, in_3);
  or or_1 (out_5, and_2_out, and_1_out);
endmodule

module ex3 (
  input  a1,
  input  b1,
  input  a0,
  input  b0,
  output out_5,
  output out_6,
  output out_7,
  output out_8
);

  wire and_1_out, and_2_out, and_3_out, meia_soma_nand_2_s1;

  and and_1 (and_1_out, a1, b1);
  and and_2 (and_2_out, a0, b1);
  Meia_soma__nand meia_soma_nand_1 (.A(and_1_out), .B(meia_soma_nand_2_s1), .s0(out_6), .s1(out_5));
  and and_3 (and_3_out, a1, b0);
  Meia_soma__nand meia_soma_nand_2 (.A(and_2_out), .B(and_3_out), .s0(out_7), .s1(meia_soma_nand_2_s1));
  and and_4 (out_8, a0, b0);
endmodule

module ex4 (
  input  A0,
  input  B0,
  input  C,
  input  A1,
  input  B1,
  output S0,
  output S1,
  output S2
);

  wire meia_soma_nand_1_s0, meia_soma_nand_1_s1, meia_soma_nand_2_s1, meia_soma_nand_3_s0,
       meia_soma_nand_3_s1, meia_soma_nand_4_s1, nand_1_out, nand_2_out, nand_3_out, nand_4_out, nand_5_out;

  Meia_soma__nand meia_soma_nand_1 (.A(A0), .B(B0), .s0(meia_soma_nand_1_s0), .s1(meia_soma_nand_1_s1));
  Meia_soma__nand meia_soma_nand_2 (.A(meia_soma_nand_1_s0), .B(C), .s0(S0), .s1(meia_soma_nand_2_s1));
  nand nand_1 (nand_1_out, meia_soma_nand_2_s1, meia_soma_nand_2_s1);
  nand nand_2 (nand_2_out, meia_soma_nand_1_s1, meia_soma_nand_1_s1);
  nand nand_3 (nand_3_out, nand_1_out, nand_2_out);
  Meia_soma__nand meia_soma_nand_3 (.A(A1), .B(B1), .s0(meia_soma_nand_3_s0), .s1(meia_soma_nand_3_s1));
  Meia_soma__nand meia_soma_nand_4 (.A(meia_soma_nand_3_s0), .B(nand_3_out), .s0(S1), .s1(meia_soma_nand_4_s1));
  nand nand_4 (nand_4_out, meia_soma_nand_4_s1, meia_soma_nand_4_s1);
  nand nand_5 (nand_5_out, meia_soma_nand_3_s1, meia_soma_nand_3_s1);
  nand nand_6 (S2, nand_4_out, nand_5_out);
endmodule

module ex5 (
  input  A0,
  input  B0,
  input  C,
  input  A1,
  input  B1,
  output S0,
  output S1,
  output S2
);

  wire \meia_diferença_nor_1_s0 , \meia_diferença_nor_1_s1 , \meia_diferença_nor_2_s1 ,
       \meia_diferença_nor_3_s0 , \meia_diferença_nor_3_s1 , \meia_diferença_nor_4_s1 , nor_1_out, nor_2_out,
       nor_3_out;

  \meia_diferença__nor  \meia_diferença_nor_1  (
    .A(A0), .B(B0), .s0(\meia_diferença_nor_1_s0 ), .s1(\meia_diferença_nor_1_s1 ));
  \meia_diferença__nor  \meia_diferença_nor_2  (
    .A(\meia_diferença_nor_1_s0 ), .B(C), .s0(S0), .s1(\meia_diferença_nor_2_s1 ));
  nor nor_1 (nor_1_out, \meia_diferença_nor_2_s1 , \meia_diferença_nor_1_s1 );
  nor nor_2 (nor_2_out, nor_1_out, nor_1_out);
  \meia_diferença__nor  \meia_diferença_nor_3  (
    .A(A1), .B(B1), .s0(\meia_diferença_nor_3_s0 ), .s1(\meia_diferença_nor_3_s1 ));
  \meia_diferença__nor  \meia_diferença_nor_4  (
    .A(\meia_diferença_nor_3_s0 ), .B(nor_2_out), .s0(S1), .s1(\meia_diferença_nor_4_s1 ));
  nor nor_3 (nor_3_out, \meia_diferença_nor_4_s1 , \meia_diferença_nor_3_s1 );
  nor nor_4 (S2, nor_3_out, nor_3_out);
endmodule
