// Logisim project Circuitos.circ as structural Verilog: 8 circuits, main circuit Meia-Soma(Comum)
module Meia_Soma_Comum (
  input  A,
  input  B,
  output S0,
  output S1
);

  wire and_1_out, and_2_out, not_1_out, not_2_out;

  not not_1 (not_1_out, A);
  not not_2 (not_2_out, B);
  and and_1 (and_1_out, not_1_out, B);
  and and_2 (and_2_out, A, not_2_out);
  and and_3 (S1, A, B);
  or or_1 (S0, and_1_out, and_2_out);
endmodule

module somaCompleta_Comum (
  input  A,
  input  B,
  input  C,
  output S0,
  output S1
);

  wire meia_soma_comum_1_s0, meia_soma_comum_1_s1, meia_soma_comum_2_s1;

  Meia_Soma_Comum meia_soma_comum_1 (.A(A), .B(B), .S0(meia_soma_comum_1_s0), .S1(meia_soma_comum_1_s1));
  Meia_Soma_Comum meia_soma_comum_2 (.A(meia_soma_comum_1_s0), .B(C), .S0(S0), .S1(meia_soma_comum_2_s1));
  or or_1 (S1, meia_soma_comum_2_s1, meia_soma_comum_1_s1);
endmodule

module \Meia_Difereça_Comum  (
  input  A,
  input  B,
  output S0,
  output S1
);

  wire and_1_out, and_2_out, not_1_out, not_2_out, not_3_out;

  not not_1 (not_1_out, A);
  not not_2 (not_2_out, B);
  not not_3 (not_3_out, A);
  and and_1 (and_1_out, not_1_out, B);
  and and_2 (and_2_out, A, not_2_out);
  and and_3 (S1, not_3_out, B);
  or or_1 (S0, and_1_out, and_2_out);
endmodule

module \diferençaCompleta  (
  input  A,
  input  B,
  input  C,
  output S0,
  output S1
);

  wire \meia_difereça_comum_1_s0 , \meia_difereça_comum_1_s1 , \meia_difereça_comum_2_s1 ;

  \Meia_Difereça_Comum  \meia_difereça_comum_1  (
    .A(A), .B(B), .S0(\meia_difereça_comum_1_s0 ), .S1(\meia_difereça_comum_1_s1 ));
  \Meia_Difereça_Comum  \meia_difereça_comum_2  (
    .A(\meia_difereça_comum_1_s0 ), .B(C), .S0(S0), .S1(\meia_difereça_comum_2_s1 ));
  or or_1 (S1, \meia_difereça_comum_2_s1 , \meia_difereça_comum_1_s1 );
endmodule

module meiaSoma_Nor (
  input  A,
  input  B,
  output S0,
  output S1
);

  wire nor_1_out, nor_2_out, nor_3_out, nor_4_out, nor_5_out, nor_6_out;

  nor nor_1 (nor_1_out, A, A);
  nor nor_2 (nor_2_out, B, B);
  nor nor_3 (nor_3_out, A, B);
  nor nor_4 (nor_4_out, A, A);
  nor nor_5 (nor_5_out, B, B);
  nor nor_6 (nor_6_out, nor_1_out, nor_2_out);
  nor nor_7 (S1, nor_4_out, nor_5_out);
  nor nor_8 (S0, nor_6_out, nor_3_out);
endmodule

module Somador_3bits (
  input  a3,
  input  a1,
  input  a0,
  input  b2,
  input  b1,
  input  b0,
  input  in_7,
  output S0,
  output S1,
  output S2,
  output S1_2
);

  wire somacompleta_comum_1_s1, somacompleta_comum_2_s1;

  somaCompleta_Comum somacompleta_comum_1 (.A(a0), .B(b0), .C(in_7), .S0(S0), .S1(somacompleta_comum_1_s1));
  somaCompleta_Comum somacompleta_comum_2 (
    .A(a1), .B(b1), .C(somacompleta_comum_1_s1), .S0(S1), .S1(somacompleta_comum_2_s1));
  somaCompleta_Comum somacompleta_comum_3 (.A(a3), .B(b2), .C(somacompleta_comum_2_s1), .S0(S2), .S1(S1_2));
endmodule

module Subtrator_3bits (
  input  in_1,
  input  in_2,
  input  in_3,
  input  in_4,
  input  in_5,
  output S1,
  output S1_2,
  output S1_3
);

  wire \diferençacompleta_1_s1 ;

  \diferençaCompleta  \diferençacompleta_1  (.A(in_3), .B(in_5), .C(in_1), .S0(S1), .S1(\diferençacompleta_1_s1 ));
  \diferençaCompleta  \diferençacompleta_2  (.A(in_2), .B(in_4), .C(\diferençacompleta_1_s1 ), .S0(S1_2), .S1(S1_3));
endmodule

module Multiplicador_2bits (
  input  a1,
  input  a0,
  input  b1,
  input  b0,
  input  in_5,
  output S0,
  output S1,
  output S2,
  output S3
);

  wire and_2_out, and_3_out, and_4_out, meia_soma_comum_1_s1;

  and and_1 (S0, a0, b0);
  and and_2 (and_2_out, a0, b1);
  and and_3 (and_3_out, a1, b0);
  and and_4 (and_4_out, a1, b1);
  Meia_Soma_Comum meia_soma_comum_1 (.A(and_2_out), .B(and_3_out), .S0(S1), .S1(meia_soma_comum_1_s1));
  somaCompleta_Comum somacompleta_comum_1 (.A(and_4_out), .B(in_5), .C(meia_soma_comum_1_s1), .S0(S2), .S1(S3));
endmodule
