// Logisim project Guia0501.circ as structural Verilog: 3 circuits, main circuit main
module main (
  input  [2:0] a,
  input  [2:0] b
);

  wire meiasoma_1_c, somacompleta_1_c;
  wire [3:0] meiasoma_1_s;

  MeiaSoma meiasoma_1 (.a(a[0]), .b(b[0]), .s(meiasoma_1_s[0]), .c(meiasoma_1_c));
  SomaCompleta somacompleta_1 (.cin(meiasoma_1_c), .a(a[1]), .b(b[1]), .s(meiasoma_1_s[1]), .c(somacompleta_1_c));
  SomaCompleta somacompleta_2 (.cin(somacompleta_1_c), .a(a[2]), .b(b[2]), .s(meiasoma_1_s[2]), .c(meiasoma_1_s[3]));
  // Probe on meiasoma_1_s

  // Notes on the sheet:
  //   Expressao Simplificada:
  //   C = A ^ B
  //   S = A&B
  //   a+b
endmodule

module MeiaSoma (
  input  a,
  input  b,
  output s,
  output c
);

  and and_1 (c, a, b);
  xor xor_1 (s, a, b);
endmodule

module SomaCompleta (
  input  cin,
  input  a,
  input  b,
  output s,
  output c
);

  wire meiasoma_1_c, meiasoma_1_s, meiasoma_2_c;

  MeiaSoma meiasoma_1 (.a(cin), .b(a), .s(meiasoma_1_s), .c(meiasoma_1_c));
  MeiaSoma meiasoma_2 (.a(meiasoma_1_s), .b(b), .s(s), .c(meiasoma_2_c));
  or or_1 (c, meiasoma_2_c, meiasoma_1_c);
endmodule
