// Logisim project Guia0502.circ as structural Verilog: 3 circuits, main circuit main
module main (
  input  [1:0] a,
  input  [1:0] b
);

  wire halfsubtractor_1_c;
  wire [2:0] halfsubtractor_1_s;

  HalfSubtractor halfsubtractor_1 (.a(a[0]), .b(b[0]), .s(halfsubtractor_1_s[0]), .c(halfsubtractor_1_c));
  FullSubtractor fullsubtractor_1 (
    .a(a[1]), .b(b[1]), .cin(halfsubtractor_1_c), .s(halfsubtractor_1_s[1]), .c(halfsubtractor_1_s[2]));
  // Probe on halfsubtractor_1_s

  // Notes on the sheet:
  //   Expressao Simplificada:
  //   S = A ^ B
  //   C = ~A & B
  //   a-b
  //   caso MSB = 1, necessário complemento de 2.
endmodule

module HalfSubtractor (
  input  a,
  input  b,
  output s,
  output c
);

  wire not_1_out;

  not not_1 (not_1_out, a);
  and and_1 (c, not_1_out, b);
  xor xor_1 (s, a, b);
endmodule

module FullSubtractor (
  input  a,
  input  b,
  input  cin,
  output s,
  output c
);

  wire halfsubtractor_1_c, halfsubtractor_1_s, halfsubtractor_2_c;

  HalfSubtractor halfsubtractor_1 (.a(a), .b(b), .s(halfsubtractor_1_s), .c(halfsubtractor_1_c));
  HalfSubtractor halfsubtractor_2 (.a(halfsubtractor_1_s), .b(cin), .s(s), .c(halfsubtractor_2_c));
  or or_1 (c, halfsubtractor_2_c, halfsubtractor_1_c);
endmodule
