// Logisim project Guia0503.circ as structural Verilog: 2 circuits, main circuit main
module main (
  input  [1:0] a,
  input  [1:0] b
);

  wire and_2_out, and_3_out, and_4_out, meiasoma_1_c;
  wire [3:0] and_1_out;

  and and_1 (and_1_out[0], a[0], b[0]);
  and and_2 (and_2_out, a[1], b[0]);
  and and_3 (and_3_out, a[0], b[1]);
  MeiaSoma meiasoma_1 (.a(and_2_out), .b(and_3_out), .s(and_1_out[1]), .c(meiasoma_1_c));
  and and_4 (and_4_out, a[1], b[1]);
  MeiaSoma meiasoma_2 (.a(meiasoma_1_c), .b(and_4_out), .s(and_1_out[2]), .c(and_1_out[3]));
  // Probe on and_1_out

  // Notes on the sheet:
  //   a*b
  //   s0 = a0&b0
  //   s3 = CarryHA2
  //   Expressao Simplificada:
  //   s1 = HA1 ( (a1&b0) + (a0&b1))
  //   s2 = HA2 (CarryHA1 + (a1&b1))
endmodule

module MeiaSoma (
  input  a,
  input  b,
  output s,
  output c
);

  and and_1 (c, a, b);
  xor xor_1 (s, a, b);
endmodule
