// Logisim project Guia0504.circ as structural Verilog: 3 circuits, main circuit main
module main (
  input  [1:0] a,
  input  [1:0] b
);

  wire meiasoma_1_c;
  wire [2:0] meiasoma_1_s;

  MeiaSoma meiasoma_1 (.a(a[0]), .b(b[0]), .s(meiasoma_1_s[0]), .c(meiasoma_1_c));
  SomaCompleta somacompleta_1 (.cin(meiasoma_1_c), .a(a[1]), .b(b[1]), .s(meiasoma_1_s[1]), .c(meiasoma_1_s[2]));
  // Probe on meiasoma_1_s

  // Notes on the sheet:
  //   a+b
  //   usando portas nand
endmodule

module MeiaSoma (
  input  a,
  input  b,
  output s,
  output c
);

  wire nand_2_out, nand_3_out, nand_4_out, nand_5_out, nand_6_out, nand_7_out, nand_8_out, nand_9_out,
       nand_10_out, nand_11_out;

  not nand_1 (c, nand_2_out);  // NAND_Gate
  nand nand_2 (nand_2_out, a, b);
  not nand_3 (nand_3_out, a);  // NAND_Gate
  nand nand_4 (nand_4_out, nand_3_out, b);
  nand nand_5 (nand_5_out, a, nand_6_out);
  not nand_6 (nand_6_out, b);  // NAND_Gate
  not nand_7 (nand_7_out, nand_4_out);  // NAND_Gate
  not nand_8 (nand_8_out, nand_5_out);  // NAND_Gate
  nand nand_9 (nand_9_out, nand_7_out, nand_8_out);
  nand nand_10 (nand_10_out, nand_7_out, nand_9_out);
  nand nand_11 (nand_11_out, nand_9_out, nand_8_out);
  nand nand_12 (s, nand_10_out, nand_11_out);
endmodule

module SomaCompleta (
  input  cin,
  input  a,
  input  b,
  output s,
  output c
);

  wire meiasoma_1_c, meiasoma_1_s, meiasoma_2_c, nand_1_out, nand_2_out;

  MeiaSoma meiasoma_1 (.a(cin), .b(a), .s(meiasoma_1_s), .c(meiasoma_1_c));
  MeiaSoma meiasoma_2 (.a(meiasoma_1_s), .b(b), .s(s), .c(meiasoma_2_c));
  not nand_1 (nand_1_out, meiasoma_2_c);  // NAND_Gate
  nand nand_2 (nand_2_out, nand_1_out, meiasoma_1_c);
  nand nand_3 (c, nand_1_out, nand_2_out);
endmodule
