// Logisim project Guia0505.circ as structural Verilog: 3 circuits, main circuit main
module main (
  input  [1:0] a,
  input  [1:0] b
);

  wire halfsubtractor_1_c;
  wire [2:0] halfsubtractor_1_out_3;

  HalfSubtractor halfsubtractor_1 (.a(a[0]), .b(b[0]), .out_3(halfsubtractor_1_out_3[0]), .c(halfsubtractor_1_c));
  FullSubtractor fullsubtractor_1 (
    .a(a[1]), .b(b[1]), .cin(halfsubtractor_1_c), .s(halfsubtractor_1_out_3[1]), .c(halfsubtractor_1_out_3[2]));
  // Probe on halfsubtractor_1_out_3

  // Notes on the sheet:
  //   a-b
  //   usando portas NOR
  //   caso MSB = 1, necessário complemento de 2.
endmodule

module HalfSubtractor (
  input  a,
  input  b,
  output out_3,
  output c
);

  wire nor_1_out, nor_2_out, nor_3_out, nor_5_out, nor_6_out, nor_7_out;

  not nor_1 (nor_1_out, b);  // NOR_Gate
  not nor_2 (nor_2_out, a);  // NOR_Gate
  not nor_3 (nor_3_out, b);  // NOR_Gate
  nor nor_4 (c, a, nor_1_out);
  nor nor_5 (nor_5_out, nor_2_out, b);
  nor nor_6 (nor_6_out, a, nor_3_out);
  nor nor_7 (nor_7_out, nor_5_out, nor_6_out);
  not nor_8 (out_3, nor_7_out);  // NOR_Gate
endmodule

module FullSubtractor (
  input  a,
  input  b,
  input  cin,
  output s,
  output c
);

  wire halfsubtractor_1_c, halfsubtractor_1_out_3, halfsubtractor_2_c, nor_1_out;

  HalfSubtractor halfsubtractor_1 (.a(a), .b(b), .out_3(halfsubtractor_1_out_3), .c(halfsubtractor_1_c));
  HalfSubtractor halfsubtractor_2 (.a(halfsubtractor_1_out_3), .b(cin), .out_3(s), .c(halfsubtractor_2_c));
  nor nor_1 (nor_1_out, halfsubtractor_2_c, halfsubtractor_1_c);
  not nor_2 (c, nor_1_out);  // NOR_Gate
endmodule
