// Logisim project Guia05_02.circ as structural Verilog: 3 circuits, main circuit Full_Subtractor
module Full_Subtractor (
  input  [1:0] Cin,
  input  [1:0] X,
  input  [1:0] Y,
  output [1:0] Cout,
  output [1:0] S
);

  wire [1:0] half_subtractor2_1_s1, half_subtractor_1_s0, half_subtractor_1_s1;

  Half_Subtractor half_subtractor_1 (.X(X), .Y(Y), .s0(half_subtractor_1_s0), .s1(half_subtractor_1_s1));
  Half_Subtractor2 half_subtractor2_1 (.X(Cin), .Y(half_subtractor_1_s0), .s0(Cout), .s1(half_subtractor2_1_s1));
  assign S = half_subtractor2_1_s1 | half_subtractor_1_s1;  // OR_Gate or_1, 2 bits wide
endmodule

module Half_Subtractor (
  input  [1:0] X,
  input  [1:0] Y,
  output [1:0] s0,
  output [1:0] s1
);

  wire [1:0] not_1_out;

  assign not_1_out = ~X;  // NOT_Gate not_1, 2 bits wide
  assign s0 = X ^ Y;  // XOR_Gate xor_1, 2 bits wide
  assign s1 = Y & not_1_out;  // AND_Gate and_1, 2 bits wide
endmodule

module Half_Subtractor2 (
  input  [1:0] X,
  input  [1:0] Y,
  output [1:0] s0,
  output [1:0] s1
);

  wire [1:0] not_1_out;

  assign not_1_out = ~X;  // NOT_Gate not_1, 2 bits wide
  assign s0 = X ^ Y;  // XOR_Gate xor_1, 2 bits wide
  assign s1 = Y & not_1_out;  // AND_Gate and_1, 2 bits wide
endmodule
