// Logisim project Guia05_05.circ as structural Verilog: 3 circuits, main circuit main
module main (
  input  B1,
  input  B0,
  input  A1,
  input  A0,
  output S2,
  output S1,
  output S0
);

  wire full_subtractor_2_cout;

  Full_Subtractor full_subtractor_1 (.B(B1), .A(A1), .Cin(full_subtractor_2_cout), .Cout(S2), .S(S1));
  Full_Subtractor full_subtractor_2 (.B(B0), .A(A0), .Cin(1'b0), .Cout(full_subtractor_2_cout), .S(S0));
endmodule

module Half_Subtractor (
  input  B,
  input  A,
  output Cout,
  output S
);

  wire nor_1_out, nor_2_out, nor_3_out, nor_5_out;

  nor nor_1 (nor_1_out, B, B);
  nor nor_2 (nor_2_out, A, A);
  nor nor_3 (nor_3_out, A, B);
  nor nor_4 (Cout, A, nor_1_out);
  nor nor_5 (nor_5_out, nor_1_out, nor_2_out);
  nor nor_6 (S, nor_5_out, nor_3_out);
endmodule

module Full_Subtractor (
  input  B,
  input  A,
  input  Cin,
  output Cout,
  output S
);

  wire half_subtractor_1_cout, half_subtractor_1_s, half_subtractor_2_cout, nor_1_out;

  Half_Subtractor half_subtractor_1 (.B(B), .A(A), .Cout(half_subtractor_1_cout), .S(half_subtractor_1_s));
  Half_Subtractor half_subtractor_2 (.B(half_subtractor_1_s), .A(Cin), .Cout(half_subtractor_2_cout), .S(S));
  nor nor_1 (nor_1_out, half_subtractor_2_cout, half_subtractor_1_cout);
  nor nor_2 (Cout, nor_1_out, nor_1_out);
endmodule
