// Logisim project Exercicio01_Logisim.circ as structural Verilog
module Half_add (
  input  A,
  input  B,
  output Q0,
  output Q1
);

  xor xor_1 (Q0, A, B);
  and and_1 (Q1, B, A);
endmodule

module Adder (
  input  C,
  input  A,
  input  B,
  output Q0,
  output Q1
);

  wire half_add_1_q0, half_add_1_q1, half_add_2_q1;

  Half_add half_add_1 (.A(A), .B(B), .Q0(half_add_1_q0), .Q1(half_add_1_q1));
  Half_add half_add_2 (.A(C), .B(half_add_1_q0), .Q0(Q0), .Q1(half_add_2_q1));
  or or_1 (Q1, half_add_2_q1, half_add_1_q1);
endmodule

module Adder_3bit (
  input  A0,
  input  A1,
  input  A2,
  input  B0,
  input  B1,
  input  B2,
  output S0,
  output S1,
  output S2,
  output S3
);

  wire adder_1_q1, half_add_1_q1;

  Half_add half_add_1 (.A(A0), .B(B0), .Q0(S0), .Q1(half_add_1_q1));
  Adder adder_1 (.C(half_add_1_q1), .A(A1), .B(B1), .Q0(S1), .Q1(adder_1_q1));
  Adder adder_2 (.C(adder_1_q1), .A(A2), .B(B2), .Q0(S2), .Q1(S3));

  // Notes on the sheet:
  //   Jonathan Felipe   Matricula: 415704
endmodule
