// Logisim project Exercicio02_Logisim.circ as structural Verilog: 4 circuits, main circuit main
module main (
  input  A0,
  input  A1,
  input  B0,
  input  B1,
  output S0,
  output S1,
  output S2
);

  wire halfsub_1_s1;

  HalfSub halfsub_1 (.B(A0), .A(B0), .S0(S0), .S1(halfsub_1_s1));
  Subtractor subtractor_1 (.Vem_um(halfsub_1_s1), .A(A1), .B(B1), .S0(S1), .out_5(S2));

  // Notes on the sheet:
  //   Jonathan Felipe    Matricula:415704
endmodule

module HalfSub (
  input  B,
  input  A,
  output S0,
  output S1
);

  wire not_1_out;

  xor xor_1 (S0, B, A);
  not not_1 (not_1_out, A);
  and and_1 (S1, not_1_out, B);
endmodule

module Subtractor (
  input  Vem_um,
  input  A,
  input  B,
  output S0,
  output out_5
);

  wire halfsub_1_s0, halfsub_1_s1, halfsub_2_s1;

  HalfSub halfsub_1 (.B(B), .A(A), .S0(halfsub_1_s0), .S1(halfsub_1_s1));
  HalfSub halfsub_2 (.B(Vem_um), .A(halfsub_1_s0), .S0(S0), .S1(halfsub_2_s1));
  or or_1 (out_5, halfsub_1_s1, halfsub_2_s1);
endmodule

module Sub_2bit (
  input  A0,
  input  A1,
  input  B0,
  input  B1,
  output S0,
  output S1,
  output S2
);

  wire halfsub_1_s1;

  HalfSub halfsub_1 (.B(A0), .A(B0), .S0(S0), .S1(halfsub_1_s1));
  Subtractor subtractor_1 (.Vem_um(halfsub_1_s1), .A(A1), .B(B1), .S0(S1), .out_5(S2));

  // Notes on the sheet:
  //   Jonathan Felipe    Matricula:415704
endmodule
