// Logisim project Exercicio03_Logisim.circ as structural Verilog
module Half_add (
  input  A,
  input  B,
  output Q0,
  output Q1
);

  xor xor_1 (Q0, A, B);
  and and_1 (Q1, B, A);
endmodule

module Adder (
  input  C,
  input  A,
  input  B,
  output Q0,
  output Q1
);

  wire half_add_1_q0, half_add_1_q1, half_add_2_q1;

  Half_add half_add_1 (.A(A), .B(B), .Q0(half_add_1_q0), .Q1(half_add_1_q1));
  Half_add half_add_2 (.A(C), .B(half_add_1_q0), .Q0(Q0), .Q1(half_add_2_q1));
  or or_1 (Q1, half_add_2_q1, half_add_1_q1);
endmodule

module Multiplicador (
  input  A0,
  input  A1,
  input  B0,
  input  B1,
  output S0,
  output S1,
  output S2,
  output S3
);

  wire adder_1_q1, and_2_out, and_3_out, and_4_out;

  and and_1 (S0, A0, B0);
  and and_2 (and_2_out, A1, B0);
  and and_3 (and_3_out, A0, B1);
  and and_4 (and_4_out, A0, B1);
  Adder adder_1 (.C(1'b0), .A(and_2_out), .B(and_3_out), .Q0(S1), .Q1(adder_1_q1));
  Adder adder_2 (.C(adder_1_q1), .A(1'b0), .B(and_4_out), .Q0(S2), .Q1(S3));

  // Notes on the sheet:
  //   Jonathan Felipe  Matricula:415704
endmodule
