// Logisim project Exercicio01.circ as structural Verilog: 4 circuits, main circuit soma
module main (
  input  a,
  input  b,
  output s0,
  output s1
);

  xor xor_1 (s0, a, b);
  and and_1 (s1, b, a);
endmodule

module soma (
  input  a,
  input  b,
  output s0,
  output s1
);

  xor xor_1 (s0, a, b);
  and and_1 (s1, b, a);
endmodule

module soma_completa (
  input  carry_in,
  input  a,
  input  b,
  output s0,
  output s1
);

  wire soma_1_s0, soma_1_s1, soma_2_s1;

  soma soma_1 (.a(a), .b(b), .s0(soma_1_s0), .s1(soma_1_s1));
  soma soma_2 (.a(carry_in), .b(soma_1_s0), .s0(s0), .s1(soma_2_s1));
  or or_1 (s1, soma_2_s1, soma_1_s1);
endmodule

module soma_3bits (
  input  a0,
  input  a1,
  input  a2,
  input  b0,
  input  b1,
  input  b2,
  output s0,
  output s1,
  output s2,
  output s3
);

  wire soma_1_s1, soma_completa_1_s1;

  soma soma_1 (.a(a0), .b(b0), .s0(s0), .s1(soma_1_s1));
  soma_completa soma_completa_1 (.carry_in(soma_1_s1), .a(a1), .b(b1), .s0(s1), .s1(soma_completa_1_s1));
  soma_completa soma_completa_2 (.carry_in(soma_completa_1_s1), .a(a2), .b(b2), .s0(s2), .s1(s3));
endmodule
