// Logisim project Exercicio02_guia5.circ as structural Verilog
module meia_diferenca (
  input  a,
  input  b,
  output s0,
  output s1
);

  wire not_1_out;

  not not_1 (not_1_out, a);
  xor xor_1 (s0, a, b);
  and and_1 (s1, b, not_1_out);
endmodule

module diferenca_completa (
  input  carry,
  input  a,
  input  b,
  output s0,
  output s1
);

  wire meia_diferenca_1_s0, meia_diferenca_1_s1, meia_diferenca_2_s1;

  meia_diferenca meia_diferenca_1 (.a(a), .b(b), .s0(meia_diferenca_1_s0), .s1(meia_diferenca_1_s1));
  meia_diferenca meia_diferenca_2 (.a(carry), .b(meia_diferenca_1_s0), .s0(s0), .s1(meia_diferenca_2_s1));
  or or_1 (s1, meia_diferenca_2_s1, meia_diferenca_1_s1);
endmodule

module \Diferença_2bits  (
  input  a0,
  input  a1,
  input  b0,
  input  b1,
  output s0,
  output s1
);

  wire meia_diferenca_1_s1;

  meia_diferenca meia_diferenca_1 (.a(a0), .b(b0), .s0(s0), .s1(meia_diferenca_1_s1));
  diferenca_completa diferenca_completa_1 (.carry(meia_diferenca_1_s1), .a(a1), .b(b1), .s0(s1));  // open: s1
endmodule
