// Logisim project Exercicio02.circ as structural Verilog: 3 circuits, main circuit meia diferença
module \meia_diferença  (
  input  a,
  input  b,
  output resp,
  output sinal
);

  wire not_1_out;

  xor xor_1 (resp, a, b);
  not not_1 (not_1_out, a);
  and and_1 (sinal, not_1_out, b);
endmodule

module \diferença_completa  (
  input  in_1,
  input  a,
  input  c,
  output resp,
  output sinal
);

  wire \meia_diferença_1_resp , \meia_diferença_1_sinal , \meia_diferença_2_sinal ;

  \meia_diferença  \meia_diferença_1  (
    .a(in_1), .b(a), .resp(\meia_diferença_1_resp ), .sinal(\meia_diferença_1_sinal ));
  \meia_diferença  \meia_diferença_2  (
    .a(\meia_diferença_1_resp ), .b(c), .resp(resp), .sinal(\meia_diferença_2_sinal ));
  or or_1 (sinal, \meia_diferença_1_sinal , \meia_diferença_2_sinal );
endmodule

module main (
  input  [1:0] a,
  input  [1:0] b,
  output [1:0] resp,
  output sinal
);

  wire \meia_diferença_1_sinal ;

  \meia_diferença  \meia_diferença_1  (.a(a[0]), .b(b[0]), .resp(resp[0]), .sinal(\meia_diferença_1_sinal ));
  \diferença_completa  \diferença_completa_1  (
    .in_1(\meia_diferença_1_sinal ), .a(a[1]), .c(b[1]), .resp(resp[1]), .sinal(sinal));
endmodule
