// Logisim project Exercicio03.circ as structural Verilog: 3 circuits, main circuit meia soma
module meia_soma (
  input  a,
  input  b,
  output resp,
  output carry_out
);

  xor xor_1 (resp, a, b);
  and and_1 (carry_out, a, b);
endmodule

module meia_completa (
  input  carry_in,
  input  a,
  input  b,
  output resp,
  output carry_out
);

  wire meia_soma_1_carry_out, meia_soma_1_resp, meia_soma_2_carry_out;

  meia_soma meia_soma_1 (.a(carry_in), .b(a), .resp(meia_soma_1_resp), .carry_out(meia_soma_1_carry_out));
  meia_soma meia_soma_2 (.a(meia_soma_1_resp), .b(b), .resp(resp), .carry_out(meia_soma_2_carry_out));
  or or_1 (carry_out, meia_soma_2_carry_out, meia_soma_1_carry_out);
endmodule

module main (
  input  [1:0] a,
  input  [1:0] b,
  output [3:0] resp
);

  wire and_2_out, and_3_out, and_4_out, meia_soma_1_carry_out;

  and and_1 (resp[0], a[0], b[0]);
  and and_2 (and_2_out, a[1], b[0]);
  and and_3 (and_3_out, a[0], b[1]);
  and and_4 (and_4_out, a[1], b[1]);
  meia_soma meia_soma_1 (.a(and_2_out), .b(and_3_out), .resp(resp[1]), .carry_out(meia_soma_1_carry_out));
  meia_soma meia_soma_2 (.a(meia_soma_1_carry_out), .b(and_4_out), .resp(resp[2]), .carry_out(resp[3]));
endmodule
