// Logisim project fulladder3bit.circ as structural Verilog: 1 circuit, main circuit main
module main (
  input  X0,
  input  Y0,
  input  X1,
  input  Y1,
  input  X2,
  input  Y2
);

  wire and_1_out, and_2_out, and_3_out, and_4_out, and_5_out, or_1_out, or_2_out, xor_1_out, xor_2_out,
       xor_3_out, xor_4_out, xor_5_out;

  xor xor_1 (xor_1_out, X0, Y0);
  and and_1 (and_1_out, Y0, X0);
  xor xor_2 (xor_2_out, X1, Y1);
  and and_2 (and_2_out, Y1, X1);
  xor xor_3 (xor_3_out, X2, Y2);
  and and_3 (and_3_out, Y2, X2);
  xor xor_4 (xor_4_out, and_1_out, xor_2_out);
  and and_4 (and_4_out, xor_2_out, and_1_out);
  xor xor_5 (xor_5_out, or_1_out, xor_3_out);
  and and_5 (and_5_out, xor_3_out, or_1_out);
  or or_1 (or_1_out, and_4_out, and_2_out);
  or or_2 (or_2_out, and_5_out, and_3_out);
  // Probe on xor_1_out
  // Probe on xor_4_out
  // Probe on xor_5_out
  // Probe on or_2_out

  // Notes on the sheet:
  //   Carry-Out (0)
  //   SUBSTITUIR PROBE POR SAIDA (VERDE)
  //   Carry-Out (1)
endmodule
