// Logisim project guia05_ex01.circ as structural Verilog: 3 circuits, main circuit main
module main (
  input  in_1,
  input  in_2,
  input  in_3,
  input  in_4,
  input  in_5,
  input  in_6,
  input  in_7,
  output out_8,
  output out_9,
  output out_10,
  output out_11
);

  wire somacompleta_1_out_5, somacompleta_2_out_5, xor_1_out, xor_2_out, xor_3_out;

  xor xor_1 (xor_1_out, in_1, in_3);
  xor xor_2 (xor_2_out, in_1, in_5);
  xor xor_3 (xor_3_out, in_1, in_7);
  somacompleta somacompleta_1 (.in_1(in_2), .in_2(xor_1_out), .in_3(in_1), .out_4(out_8), .out_5(somacompleta_1_out_5));
  somacompleta somacompleta_2 (
    .in_1(in_4), .in_2(xor_2_out), .in_3(somacompleta_1_out_5), .out_4(out_9), .out_5(somacompleta_2_out_5));
  somacompleta somacompleta_3 (
    .in_1(in_6), .in_2(xor_3_out), .in_3(somacompleta_2_out_5), .out_4(out_10), .out_5(out_11));
endmodule

module meiasoma (
  input  in_1,
  input  in_2,
  output out_3,
  output out_4
);

  xor xor_1 (out_3, in_1, in_2);
  and and_1 (out_4, in_2, in_1);
endmodule

module somacompleta (
  input  in_1,
  input  in_2,
  input  in_3,
  output out_4,
  output out_5
);

  wire meiasoma_1_out_3, meiasoma_1_out_4, meiasoma_2_out_4;

  meiasoma meiasoma_1 (.in_1(in_1), .in_2(in_2), .out_3(meiasoma_1_out_3), .out_4(meiasoma_1_out_4));
  meiasoma meiasoma_2 (.in_1(meiasoma_1_out_3), .in_2(in_3), .out_3(out_4), .out_4(meiasoma_2_out_4));
  or or_1 (out_5, meiasoma_2_out_4, meiasoma_1_out_4);
endmodule
