// Logisim project guia05_ex02.circ as structural Verilog: 3 circuits, main circuit main
module main (
  input  in_1,
  input  in_2,
  input  in_3,
  input  in_4,
  output out_5,
  output out_6,
  output out_7
);

  wire meiadiferenca_1_out_4;

  meiadiferenca meiadiferenca_1 (.in_1(in_1), .in_2(in_2), .out_3(out_5), .out_4(meiadiferenca_1_out_4));
  diferencacompleta diferencacompleta_1 (
    .in_1(in_3), .in_2(in_4), .in_3(meiadiferenca_1_out_4), .out_4(out_6), .out_5(out_7));
endmodule

module meiadiferenca (
  input  in_1,
  input  in_2,
  output out_3,
  output out_4
);

  wire not_1_out;

  not not_1 (not_1_out, in_1);
  xor xor_1 (out_3, in_1, in_2);
  and and_1 (out_4, not_1_out, in_2);
endmodule

module diferencacompleta (
  input  in_1,
  input  in_2,
  input  in_3,
  output out_4,
  output out_5
);

  wire meiadiferenca_1_out_3, meiadiferenca_1_out_4, meiadiferenca_2_out_4;

  meiadiferenca meiadiferenca_1 (
    .in_1(in_1), .in_2(in_2), .out_3(meiadiferenca_1_out_3), .out_4(meiadiferenca_1_out_4));
  meiadiferenca meiadiferenca_2 (
    .in_1(meiadiferenca_1_out_3), .in_2(in_3), .out_3(out_5), .out_4(meiadiferenca_2_out_4));
  or or_1 (out_4, meiadiferenca_2_out_4, meiadiferenca_1_out_4);
endmodule
