// Logisim project guia05_ex03.circ as structural Verilog: 1 circuit, main circuit main
module main (
  input  in_1,
  input  in_2,
  input  in_3,
  input  in_4,
  output out_5,
  output out_6,
  output out_7,
  output out_8
);

  wire and_1_out, and_3_out, and_4_out, not_1_out;

  and and_1 (and_1_out, in_1, in_3);
  and and_2 (out_8, in_2, in_4);
  and and_3 (and_3_out, in_1, in_4);
  and and_4 (and_4_out, in_2, in_3);
  and and_5 (out_5, and_1_out, out_8);
  not not_1 (not_1_out, out_8);
  and and_6 (out_6, and_1_out, not_1_out);
  xor xor_1 (out_7, and_3_out, and_4_out);
endmodule
