// Logisim project guia05_ex04.circ as structural Verilog: 7 circuits, main circuit main
module main (
  input  in_1,
  input  in_2,
  input  in_3,
  input  in_4,
  input  in_5,
  input  in_6,
  input  in_7,
  output out_8,
  output out_9,
  output out_10,
  output out_11
);

  wire somacompleta_1_out_5, somacompleta_2_out_5, xor_1_out_3, xor_2_out_3, xor_3_out_3;

  \xor  xor_1 (.in_1(in_1), .in_2(in_3), .out_3(xor_1_out_3));
  \xor  xor_2 (.in_1(in_1), .in_2(in_5), .out_3(xor_2_out_3));
  \xor  xor_3 (.in_1(in_1), .in_2(in_7), .out_3(xor_3_out_3));
  somacompleta somacompleta_1 (
    .in_1(in_2), .in_2(xor_1_out_3), .in_3(in_1), .out_4(out_8), .out_5(somacompleta_1_out_5));
  somacompleta somacompleta_2 (
    .in_1(in_4), .in_2(xor_2_out_3), .in_3(somacompleta_1_out_5), .out_4(out_9), .out_5(somacompleta_2_out_5));
  somacompleta somacompleta_3 (
    .in_1(in_6), .in_2(xor_3_out_3), .in_3(somacompleta_2_out_5), .out_4(out_10), .out_5(out_11));
endmodule

module \or  (
  input  in_1,
  input  in_2,
  output out_3
);

  wire nand_1_out, nand_2_out;

  nand nand_1 (nand_1_out, in_1, in_1);
  nand nand_2 (nand_2_out, in_2, in_2);
  nand nand_3 (out_3, nand_1_out, nand_2_out);
endmodule

module \and  (
  input  in_1,
  input  in_2,
  output out_3
);

  wire nand_1_out;

  nand nand_1 (nand_1_out, in_1, in_2);
  nand nand_2 (out_3, nand_1_out, nand_1_out);
endmodule

module \not  (
  input  in_1,
  output out_2
);

  nand nand_1 (out_2, in_1, in_1);
endmodule

module \xor  (
  input  in_1,
  input  in_2,
  output out_3
);

  wire and_1_out_3, and_2_out_3, not_1_out_2, not_2_out_2;

  \not  not_1 (.in_1(in_2), .out_2(not_1_out_2));
  \not  not_2 (.in_1(in_1), .out_2(not_2_out_2));
  \and  and_1 (.in_1(in_1), .in_2(not_1_out_2), .out_3(and_1_out_3));
  \and  and_2 (.in_1(not_2_out_2), .in_2(in_2), .out_3(and_2_out_3));
  \or  or_1 (.in_1(and_1_out_3), .in_2(and_2_out_3), .out_3(out_3));
endmodule

module meiasoma (
  input  in_1,
  input  in_2,
  output out_3,
  output out_4
);

  \xor  xor_1 (.in_1(in_1), .in_2(in_2), .out_3(out_3));
  \and  and_1 (.in_1(in_1), .in_2(in_2), .out_3(out_4));
endmodule

module somacompleta (
  input  in_1,
  input  in_2,
  input  in_3,
  output out_4,
  output out_5
);

  wire meiasoma_1_out_3, meiasoma_1_out_4, meiasoma_2_out_4;

  meiasoma meiasoma_1 (.in_1(in_1), .in_2(in_2), .out_3(meiasoma_1_out_3), .out_4(meiasoma_1_out_4));
  meiasoma meiasoma_2 (.in_1(meiasoma_1_out_3), .in_2(in_3), .out_3(out_4), .out_4(meiasoma_2_out_4));
  \or  or_1 (.in_1(meiasoma_2_out_4), .in_2(meiasoma_1_out_4), .out_3(out_5));
endmodule
