// Logisim project guia05_ex05.circ as structural Verilog: 7 circuits, main circuit main
module main (
  input  in_1,
  input  in_2,
  input  in_3,
  input  in_4,
  input  in_5,
  input  in_6,
  output out_7,
  output out_8,
  output out_9,
  output out_10
);

  wire diferencacompleta_1_out_5, meiadiferenca_1_out_4;

  meiadiferenca meiadiferenca_1 (.in_1(in_1), .in_2(in_2), .out_3(out_7), .out_4(meiadiferenca_1_out_4));
  diferencacompleta diferencacompleta_1 (
    .in_1(in_3), .in_2(in_4), .in_3(meiadiferenca_1_out_4), .out_4(out_8), .out_5(diferencacompleta_1_out_5));
  diferencacompleta diferencacompleta_2 (
    .in_1(in_5), .in_2(in_6), .in_3(diferencacompleta_1_out_5), .out_4(out_9), .out_5(out_10));
endmodule

module \not  (
  input  in_1,
  output out_2
);

  nor nor_1 (out_2, in_1, in_1);
endmodule

module \and  (
  input  in_1,
  input  in_2,
  output out_3
);

  wire nor_1_out, nor_2_out;

  nor nor_1 (nor_1_out, in_1, in_1);
  nor nor_2 (nor_2_out, in_2, in_2);
  nor nor_3 (out_3, nor_1_out, nor_2_out);
endmodule

module \or  (
  input  in_1,
  input  in_2,
  output out_3
);

  wire nor_1_out;

  nor nor_1 (nor_1_out, in_1, in_2);
  nor nor_2 (out_3, nor_1_out, nor_1_out);
endmodule

module \xor  (
  input  in_1,
  input  in_2,
  output out_3
);

  wire and_1_out_3, and_2_out_3, not_1_out_2, not_2_out_2;

  \and  and_1 (.in_1(in_1), .in_2(not_1_out_2), .out_3(and_1_out_3));
  \not  not_1 (.in_1(in_1), .out_2(not_1_out_2));
  \and  and_2 (.in_1(in_2), .in_2(not_2_out_2), .out_3(and_2_out_3));
  \not  not_2 (.in_1(in_2), .out_2(not_2_out_2));
  \or  or_1 (.in_1(and_1_out_3), .in_2(and_2_out_3), .out_3(out_3));
endmodule

module meiadiferenca (
  input  in_1,
  input  in_2,
  output out_3,
  output out_4
);

  wire not_1_out_2;

  \xor  xor_1 (.in_1(in_1), .in_2(in_2), .out_3(out_3));
  \not  not_1 (.in_1(in_1), .out_2(not_1_out_2));
  \and  and_1 (.in_1(not_1_out_2), .in_2(in_2), .out_3(out_4));
endmodule

module diferencacompleta (
  input  in_1,
  input  in_2,
  input  in_3,
  output out_4,
  output out_5
);

  wire meiadiferenca_1_out_3, meiadiferenca_1_out_4, meiadiferenca_2_out_4;

  meiadiferenca meiadiferenca_1 (
    .in_1(in_1), .in_2(in_2), .out_3(meiadiferenca_1_out_3), .out_4(meiadiferenca_1_out_4));
  meiadiferenca meiadiferenca_2 (
    .in_1(meiadiferenca_1_out_3), .in_2(in_3), .out_3(out_5), .out_4(meiadiferenca_2_out_4));
  \xor  xor_1 (.in_1(meiadiferenca_2_out_4), .in_2(meiadiferenca_1_out_4), .out_3(out_4));
endmodule
