// Logisim project Exercicio01.circ as structural Verilog: 3 circuits, main circuit meia soma
module meia_soma (
  input  a,
  input  b,
  output resp,
  output carry_out
);

  xor xor_1 (resp, a, b);
  and and_1 (carry_out, a, b);
endmodule

module meia_completa (
  input  carry_in,
  input  a,
  input  b,
  output resp,
  output carry_out
);

  wire meia_soma_1_carry_out, meia_soma_1_resp, meia_soma_2_carry_out;

  meia_soma meia_soma_1 (.a(carry_in), .b(a), .resp(meia_soma_1_resp), .carry_out(meia_soma_1_carry_out));
  meia_soma meia_soma_2 (.a(meia_soma_1_resp), .b(b), .resp(resp), .carry_out(meia_soma_2_carry_out));
  or or_1 (carry_out, meia_soma_2_carry_out, meia_soma_1_carry_out);
endmodule

module main (
  input  [2:0] a,
  input  [2:0] b,
  output [2:0] resp,
  output carry_out
);

  wire meia_completa_1_carry_out, meia_soma_1_carry_out;

  meia_soma meia_soma_1 (.a(a[0]), .b(b[0]), .resp(resp[0]), .carry_out(meia_soma_1_carry_out));
  meia_completa meia_completa_1 (
    .carry_in(meia_soma_1_carry_out), .a(a[1]), .b(b[1]), .resp(resp[1]),
    .carry_out(meia_completa_1_carry_out));
  meia_completa meia_completa_2 (
    .carry_in(meia_completa_1_carry_out), .a(a[2]), .b(b[2]), .resp(resp[2]), .carry_out(carry_out));
endmodule
