// Logisim project Exercicio01.circ as structural Verilog: 3 circuits, main circuit main
module main (
  input  a0,
  input  b0,
  input  a1,
  input  b1,
  input  a2,
  input  b2,
  output s0,
  output s1,
  output s2,
  output Carry
);

  wire full_adder_1_out_5, half_adder_1_out_4;

  Half_adder half_adder_1 (.in_1(a0), .in_2(b0), .out_3(s0), .out_4(half_adder_1_out_4));
  Full_adder full_adder_1 (.in_1(half_adder_1_out_4), .in_2(a1), .in_3(b1), .out_4(s1), .out_5(full_adder_1_out_5));
  Full_adder full_adder_2 (.in_1(full_adder_1_out_5), .in_2(a2), .in_3(b2), .out_4(s2), .out_5(Carry));
endmodule

module Half_adder (
  input  in_1,
  input  in_2,
  output out_3,
  output out_4
);

  xor xor_1 (out_3, in_1, in_2);
  and and_1 (out_4, in_1, in_2);
endmodule

module Full_adder (
  input  in_1,
  input  in_2,
  input  in_3,
  output out_4,
  output out_5
);

  wire half_adder_1_out_3, half_adder_1_out_4, half_adder_2_out_4;

  Half_adder half_adder_1 (.in_1(in_1), .in_2(in_2), .out_3(half_adder_1_out_3), .out_4(half_adder_1_out_4));
  Half_adder half_adder_2 (.in_1(half_adder_1_out_3), .in_2(in_3), .out_3(out_4), .out_4(half_adder_2_out_4));
  or or_1 (out_5, half_adder_2_out_4, half_adder_1_out_4);
endmodule
