// Logisim project Exercicio02.circ as structural Verilog: 3 circuits, main circuit main
module main (
  input  a0,
  input  b0,
  input  a1,
  input  b1,
  input  a2,
  input  b2,
  output [2:0] out_7,
  output out_8
);

  wire full_subtractor_1_out_5, half_subtractor_1_c;

  Half_Subtractor half_subtractor_1 (.a(a0), .b(b0), .s(out_7[0]), .c(half_subtractor_1_c));
  Full_Subtractor full_subtractor_1 (
    .a(a1), .b(b1), .c(half_subtractor_1_c), .out_4(out_7[1]), .out_5(full_subtractor_1_out_5));
  Full_Subtractor full_subtractor_2 (.a(a2), .b(b2), .c(full_subtractor_1_out_5), .out_4(out_7[2]), .out_5(out_8));
endmodule

module Half_Subtractor (
  input  a,
  input  b,
  output s,
  output c
);

  wire not_1_out;

  xor xor_1 (s, a, b);
  not not_1 (not_1_out, a);
  and and_1 (c, not_1_out, b);
endmodule

module Full_Subtractor (
  input  a,
  input  b,
  input  c,
  output out_4,
  output out_5
);

  wire half_subtractor_1_c, half_subtractor_1_s, half_subtractor_2_c;

  Half_Subtractor half_subtractor_1 (.a(a), .b(b), .s(half_subtractor_1_s), .c(half_subtractor_1_c));
  Half_Subtractor half_subtractor_2 (.a(half_subtractor_1_s), .b(c), .s(out_4), .c(half_subtractor_2_c));
  or or_1 (out_5, half_subtractor_2_c, half_subtractor_1_c);
endmodule
