// Logisim project Exercicio03.circ as structural Verilog: 3 circuits, main circuit main
module main (
  input  a1,
  input  a0,
  input  b1,
  input  b0,
  output out_5,
  output out_6,
  output out_7,
  output out_8
);

  wire and_2_out, and_3_out, and_4_out, half_adder_1_c_out;

  and and_1 (out_8, b0, a0);
  and and_2 (and_2_out, a0, b1);
  and and_3 (and_3_out, a1, b0);
  and and_4 (and_4_out, a1, b1);
  Half_Adder half_adder_1 (.a(and_2_out), .b(and_3_out), .s(out_7), .c_out(half_adder_1_c_out));
  Full_Adder full_adder_1 (.a(half_adder_1_c_out), .b(1'b0), .c(and_4_out), .s(out_6), .c_out(out_5));
endmodule

module Half_Adder (
  input  a,
  input  b,
  output s,
  output c_out
);

  xor xor_1 (s, a, b);
  and and_1 (c_out, a, b);
endmodule

module Full_Adder (
  input  a,
  input  b,
  input  c,
  output s,
  output c_out
);

  wire half_adder_1_c_out, half_adder_1_s, half_adder_2_c_out;

  Half_Adder half_adder_1 (.a(a), .b(b), .s(half_adder_1_s), .c_out(half_adder_1_c_out));
  Half_Adder half_adder_2 (.a(half_adder_1_s), .b(c), .s(s), .c_out(half_adder_2_c_out));
  or or_1 (c_out, half_adder_2_c_out, half_adder_1_c_out);
endmodule
