// Logisim project exercicio01.circ as structural Verilog: 5 circuits, main circuit main
module main (
  input  Sinal,
  input  [2:0] a,
  input  Sinal_2,
  input  [2:0] b,
  output Igual,
  output [3:0] Resultado,
  output Overflow
);

  equals equals_1 (
    .in_1(a[0]), .in_2(a[1]), .in_3(a[2]), .in_4(Sinal), .in_5(b[0]), .in_6(b[1]), .in_7(b[2]),
    .in_8(Sinal_2), .out_9(Igual));
  complete_adder complete_adder_1 (
    .a0(a[0]), .a1(a[1]), .a2(a[2]), .sinal1(Sinal), .b0(b[0]), .b1(b[1]), .b2(b[2]), .sinal2(Sinal_2),
    .Resultado(Resultado), .Overflow(Overflow));

  // Notes on the sheet:
  //   Guia_06 - Exercicio01
  //   Projeto de uma ALU de 4 bits com somador completo e comparador
  //   Autor: Tiago Menegaz de Melo Garcia
  //   Matrícula: 405844
endmodule

module equals (
  input  in_1,
  input  in_2,
  input  in_3,
  input  in_4,
  input  in_5,
  input  in_6,
  input  in_7,
  input  in_8,
  output out_9
);

  wire xnor_1_out, xnor_2_out, xnor_3_out, xnor_4_out;

  xnor xnor_1 (xnor_1_out, in_1, in_5);
  xnor xnor_2 (xnor_2_out, in_2, in_6);
  xnor xnor_3 (xnor_3_out, in_3, in_7);
  xnor xnor_4 (xnor_4_out, in_4, in_8);
  and and_1 (out_9, xnor_1_out, xnor_2_out, xnor_3_out, xnor_4_out);
endmodule

module full_adder (
  input  vem_um,
  input  a,
  input  b,
  output Resto,
  output Vai_um
);

  wire and_1_out, and_2_out, xor_1_out;

  xor xor_1 (xor_1_out, a, b);
  and and_1 (and_1_out, b, a);
  xor xor_2 (Resto, vem_um, xor_1_out);
  and and_2 (and_2_out, vem_um, xor_1_out);
  or or_1 (Vai_um, and_2_out, and_1_out);
endmodule

module half_adder (
  input  a,
  input  b,
  output Resto,
  output Vai_um
);

  xor xor_1 (Resto, a, b);
  and and_1 (Vai_um, b, a);
endmodule

module complete_adder (
  input  a0,
  input  a1,
  input  a2,
  input  sinal1,
  input  b0,
  input  b1,
  input  b2,
  input  sinal2,
  output [3:0] Resultado,
  output Overflow
);

  wire full_adder_1_vai_um, full_adder_2_vai_um, full_adder_3_vai_um, half_adder_1_vai_um;

  half_adder half_adder_1 (.a(a0), .b(b0), .Resto(Resultado[0]), .Vai_um(half_adder_1_vai_um));
  full_adder full_adder_1 (
    .vem_um(half_adder_1_vai_um), .a(a1), .b(b1), .Resto(Resultado[1]), .Vai_um(full_adder_1_vai_um));
  full_adder full_adder_2 (
    .vem_um(full_adder_1_vai_um), .a(a2), .b(b2), .Resto(Resultado[2]), .Vai_um(full_adder_2_vai_um));
  full_adder full_adder_3 (
    .vem_um(full_adder_2_vai_um), .a(sinal1), .b(sinal2), .Resto(Resultado[3]), .Vai_um(full_adder_3_vai_um));
  xor xor_1 (Overflow, Resultado[3], full_adder_3_vai_um);
endmodule
