// Logisim project exercicio04.circ as structural Verilog: 10 circuits, main circuit main
module main (
  input  Sinal,
  input  [2:0] a,
  input  Sinal_2,
  input  [2:0] b,
  output Igual,
  output [3:0] Resultado,
  output [3:0] Complemento_de_um_do_resultado,
  output Overflow,
  output Carry,
  output Zero,
  output [3:0] Resultado_2,
  output [3:0] Complemento_de_um_do_Resultado_2,
  output Overflow_2,
  output Carry_2,
  output Zero_2
);

  equals equals_1 (
    .in_1(a[0]), .in_2(a[1]), .in_3(a[2]), .in_4(Sinal), .in_5(b[0]), .in_6(b[1]), .in_7(b[2]),
    .in_8(Sinal_2), .out_9(Igual));
  complete_adder complete_adder_1 (
    .a0(a[0]), .a1(a[1]), .a2(a[2]), .sinal(Sinal), .b0(b[0]), .b1(b[1]), .b2(b[2]), .sinal_2(Sinal_2),
    .Resultado(Resultado), .Overflow(Overflow), .Carry(Carry), .Zero(Zero));
  complete_subtractor complete_subtractor_1 (
    .a0(a[0]), .a1(a[1]), .a2(a[2]), .sinal(Sinal), .b0(b[0]), .b1(b[1]), .b2(b[2]), .sinal_2(Sinal_2),
    .Resultado(Resultado_2), .Vem_um(Overflow_2), .Carry(Carry_2), .Zero(Zero_2));
  complemento1 complemento1_1 (.in_1(Resultado), .complemento(Complemento_de_um_do_resultado));
  complemento1 complemento1_2 (.in_1(Resultado_2), .complemento(Complemento_de_um_do_Resultado_2));

  // Notes on the sheet:
  //   Guia_06 - Exercicio04
  //   Autor: Tiago Menegaz de Melo Garcia
  //   Inclusão em uma ALU de 4 bits cálculo do complemento de um
  //   Matrícula: 405844
endmodule

module equals (
  input  in_1,
  input  in_2,
  input  in_3,
  input  in_4,
  input  in_5,
  input  in_6,
  input  in_7,
  input  in_8,
  output out_9
);

  wire xnor_1_out, xnor_2_out, xnor_3_out, xnor_4_out;

  xnor xnor_1 (xnor_1_out, in_1, in_5);
  xnor xnor_2 (xnor_2_out, in_2, in_6);
  xnor xnor_3 (xnor_3_out, in_3, in_7);
  xnor xnor_4 (xnor_4_out, in_4, in_8);
  and and_1 (out_9, xnor_1_out, xnor_2_out, xnor_3_out, xnor_4_out);
endmodule

module full_adder (
  input  vem_um,
  input  a,
  input  b,
  output Resto,
  output Vai_um
);

  wire and_1_out, and_2_out, xor_1_out;

  xor xor_1 (xor_1_out, a, b);
  and and_1 (and_1_out, b, a);
  xor xor_2 (Resto, vem_um, xor_1_out);
  and and_2 (and_2_out, vem_um, xor_1_out);
  or or_1 (Vai_um, and_2_out, and_1_out);
endmodule

module half_adder (
  input  a,
  input  b,
  output Resto,
  output Vai_um
);

  xor xor_1 (Resto, a, b);
  and and_1 (Vai_um, b, a);
endmodule

module complete_adder (
  input  a0,
  input  a1,
  input  a2,
  input  sinal,
  input  b0,
  input  b1,
  input  b2,
  input  sinal_2,
  output [3:0] Resultado,
  output Overflow,
  output Carry,
  output Zero
);

  wire full_adder_1_vai_um, full_adder_3_vai_um, half_adder_1_vai_um;

  half_adder half_adder_1 (.a(a0), .b(b0), .Resto(Resultado[0]), .Vai_um(half_adder_1_vai_um));
  full_adder full_adder_1 (
    .vem_um(half_adder_1_vai_um), .a(a1), .b(b1), .Resto(Resultado[1]), .Vai_um(full_adder_1_vai_um));
  full_adder full_adder_2 (.vem_um(full_adder_1_vai_um), .a(a2), .b(b2), .Resto(Resultado[2]), .Vai_um(Carry));
  full_adder full_adder_3 (.vem_um(Carry), .a(sinal), .b(sinal_2), .Resto(Resultado[3]), .Vai_um(full_adder_3_vai_um));
  xor xor_1 (Overflow, Resultado[3], full_adder_3_vai_um);
  nor nor_1 (Zero, Resultado[2], Resultado[1], Resultado[0]);
endmodule

module half_subtractor (
  input  a,
  input  b,
  output Resto,
  output Vem_um
);

  wire buffer_1_out;

  buf buffer_1 (buffer_1_out, a);
  xor xor_1 (Resto, a, b);
  and and_1 (Vem_um, b, buffer_1_out);
endmodule

module full_subtractor (
  input  Vem_um,
  input  a,
  input  b,
  output Resto,
  output Vem_um_2
);

  wire and_1_out, and_2_out, buffer_1_out, buffer_2_out, xor_1_out;

  xor xor_1 (xor_1_out, b, a);
  and and_1 (and_1_out, b, buffer_1_out);
  buf buffer_1 (buffer_1_out, a);
  xor xor_2 (Resto, Vem_um, xor_1_out);
  and and_2 (and_2_out, Vem_um, buffer_2_out);
  buf buffer_2 (buffer_2_out, xor_1_out);
  or or_1 (Vem_um_2, and_2_out, and_1_out);
endmodule

module complete_subtractor (
  input  a0,
  input  a1,
  input  a2,
  input  sinal,
  input  b0,
  input  b1,
  input  b2,
  input  sinal_2,
  output [3:0] Resultado,
  output Vem_um,
  output Carry,
  output Zero
);

  wire full_subtractor_1_vem_um_2, full_subtractor_3_vem_um_2, full_subtractor_4_resto,
       full_subtractor_4_vem_um_2, full_subtractor_5_resto, full_subtractor_5_vem_um_2,
       full_subtractor_6_resto, half_subtractor_1_vem_um, half_subtractor_2_resto, half_subtractor_2_vem_um,
       not_1_out, not_2_out, not_3_out, not_4_out, not_5_out;

  not not_1 (not_1_out, b0);
  not not_2 (not_2_out, b1);
  not not_3 (not_3_out, b2);
  not not_4 (not_4_out, sinal_2);
  not not_5 (not_5_out, 1'b1);
  half_subtractor half_subtractor_1 (
    .a(a0), .b(half_subtractor_2_resto), .Resto(Resultado[0]), .Vem_um(half_subtractor_1_vem_um));
  full_subtractor full_subtractor_1 (
    .Vem_um(half_subtractor_1_vem_um), .a(a1), .b(full_subtractor_4_resto), .Resto(Resultado[1]),
    .Vem_um_2(full_subtractor_1_vem_um_2));
  full_subtractor full_subtractor_2 (
    .Vem_um(full_subtractor_1_vem_um_2), .a(a2), .b(full_subtractor_5_resto), .Resto(Resultado[2]),
    .Vem_um_2(Carry));
  full_subtractor full_subtractor_3 (
    .Vem_um(Carry), .a(sinal), .b(full_subtractor_6_resto), .Resto(Resultado[3]),
    .Vem_um_2(full_subtractor_3_vem_um_2));
  half_subtractor half_subtractor_2 (
    .a(not_1_out), .b(1'b1), .Resto(half_subtractor_2_resto), .Vem_um(half_subtractor_2_vem_um));
  full_subtractor full_subtractor_4 (
    .Vem_um(half_subtractor_2_vem_um), .a(not_2_out), .b(not_5_out), .Resto(full_subtractor_4_resto),
    .Vem_um_2(full_subtractor_4_vem_um_2));
  full_subtractor full_subtractor_5 (
    .Vem_um(full_subtractor_4_vem_um_2), .a(not_3_out), .b(not_5_out), .Resto(full_subtractor_5_resto),
    .Vem_um_2(full_subtractor_5_vem_um_2));
  full_subtractor full_subtractor_6 (
    .Vem_um(full_subtractor_5_vem_um_2), .a(not_4_out), .b(not_5_out), .Resto(full_subtractor_6_resto));  // open: Vem_um_2
  xor xor_1 (Vem_um, Resultado[3], full_subtractor_3_vem_um_2);
  nor nor_1 (Zero, Resultado[2], Resultado[0], Resultado[2]);
endmodule

module comparador (
  input  a0,
  input  a1,
  input  a2,
  input  Sinal,
  input  b0,
  input  b1,
  input  b2,
  input  Sinal_2
);

  // NOT_Gate not_1 has open pins: in=a0, out=open
  // NOT_Gate not_2 has open pins: in=a1, out=open
  // NOT_Gate not_3 has open pins: in=a2, out=open
  // NOT_Gate not_4 has open pins: in=Sinal, out=open
  // NOT_Gate not_5 has open pins: in=b0, out=open
  // NOT_Gate not_6 has open pins: in=b1, out=open
  // NOT_Gate not_7 has open pins: in=b2, out=open
  // NOT_Gate not_8 has open pins: in=Sinal_2, out=open
endmodule

module complemento1 (
  input  [3:0] in_1,
  output [3:0] complemento
);

  assign complemento = ~in_1;  // NOT_Gate not_1, 4 bits wide
endmodule
