// Logisim project exercicio05.circ as structural Verilog: 12 circuits, main circuit main
module main (
  input  Sinal,
  input  [2:0] a,
  input  Sinal_2,
  input  [2:0] b,
  output Igual,
  output [2:0] Resultado,
  output [2:0] Complemento_de_um_do_Resultado,
  output And_Resultado,
  output Or_Resultado,
  output Overflow,
  output [2:0] Resultado_2,
  output [2:0] Complemento_de_um_do_Resultado_2,
  output And_Resultado_2,
  output Or_Resultado_2,
  output Sinal_3
);

  equals equals_1 (
    .in_1(a[0]), .in_2(a[1]), .in_3(a[2]), .in_4(Sinal), .in_5(b[0]), .in_6(b[1]), .in_7(b[2]),
    .in_8(Sinal_2), .out_9(Igual));
  complete_adder complete_adder_1 (
    .a0(a[0]), .a1(a[1]), .a2(a[2]), .b0(b[0]), .b1(b[1]), .b2(b[2]), .Resultado(Resultado),
    .Overflow(Overflow));
  complete_subtractor complete_subtractor_1 (
    .a0(b[0]), .a1(b[1]), .a2(b[2]), .b0(a[0]), .b1(a[1]), .b2(a[2]), .Resultado(Resultado_2),
    .Vem_um(Sinal_3));
  complemento1 complemento1_1 (.in_1(Resultado), .complemento(Complemento_de_um_do_Resultado));
  \and  and_1 (.in_1(Resultado), .out_2(And_Resultado));
  \or  or_1 (.in_1(Resultado), .out_2(Or_Resultado));
  complemento1 complemento1_2 (.in_1(Resultado_2), .complemento(Complemento_de_um_do_Resultado_2));
  \and  and_2 (.in_1(Resultado_2), .out_2(And_Resultado_2));
  \or  or_2 (.in_1(Resultado_2), .out_2(Or_Resultado_2));

  // Notes on the sheet:
  //   Guia_06 - Exercicio05
  //   Inclusão em uma ALU de 4 bits OR e AND
  //   Autor: Tiago Menegaz de Melo Garcia
  //   Matrícula: 405844
endmodule

module equals (
  input  in_1,
  input  in_2,
  input  in_3,
  input  in_4,
  input  in_5,
  input  in_6,
  input  in_7,
  input  in_8,
  output out_9
);

  wire xnor_1_out, xnor_2_out, xnor_3_out, xnor_4_out;

  xnor xnor_1 (xnor_1_out, in_1, in_5);
  xnor xnor_2 (xnor_2_out, in_2, in_6);
  xnor xnor_3 (xnor_3_out, in_3, in_7);
  xnor xnor_4 (xnor_4_out, in_4, in_8);
  and and_1 (out_9, xnor_1_out, xnor_2_out, xnor_3_out, xnor_4_out);
endmodule

module full_adder (
  input  vem_um,
  input  a,
  input  b,
  output Resto,
  output Vai_um
);

  wire and_1_out, and_2_out, xor_1_out;

  xor xor_1 (xor_1_out, a, b);
  and and_1 (and_1_out, b, a);
  xor xor_2 (Resto, vem_um, xor_1_out);
  and and_2 (and_2_out, vem_um, xor_1_out);
  or or_1 (Vai_um, and_2_out, and_1_out);
endmodule

module half_adder (
  input  a,
  input  b,
  output Resto,
  output Vai_um
);

  xor xor_1 (Resto, a, b);
  and and_1 (Vai_um, b, a);
endmodule

module complete_adder (
  input  a0,
  input  a1,
  input  a2,
  input  b0,
  input  b1,
  input  b2,
  output [2:0] Resultado,
  output Overflow
);

  wire full_adder_1_vai_um, half_adder_1_vai_um;

  half_adder half_adder_1 (.a(a0), .b(b0), .Resto(Resultado[0]), .Vai_um(half_adder_1_vai_um));
  full_adder full_adder_1 (
    .vem_um(half_adder_1_vai_um), .a(a1), .b(b1), .Resto(Resultado[1]), .Vai_um(full_adder_1_vai_um));
  full_adder full_adder_2 (.vem_um(full_adder_1_vai_um), .a(a2), .b(b2), .Resto(Resultado[2]), .Vai_um(Overflow));
endmodule

module half_subtractor (
  input  a,
  input  b,
  output Resto,
  output Vem_um
);

  wire buffer_1_out;

  buf buffer_1 (buffer_1_out, a);
  xor xor_1 (Resto, a, b);
  and and_1 (Vem_um, b, buffer_1_out);
endmodule

module full_subtractor (
  input  Vem_um,
  input  a,
  input  b,
  output Resto,
  output Vem_um_2
);

  wire and_1_out, and_2_out, buffer_1_out, buffer_2_out, xor_1_out;

  xor xor_1 (xor_1_out, b, a);
  and and_1 (and_1_out, b, buffer_1_out);
  buf buffer_1 (buffer_1_out, a);
  xor xor_2 (Resto, Vem_um, xor_1_out);
  and and_2 (and_2_out, Vem_um, buffer_2_out);
  buf buffer_2 (buffer_2_out, xor_1_out);
  or or_1 (Vem_um_2, and_2_out, and_1_out);
endmodule

module complete_subtractor (
  input  a0,
  input  a1,
  input  a2,
  input  b0,
  input  b1,
  input  b2,
  output [2:0] Resultado,
  output Vem_um
);

  wire full_subtractor_1_vem_um_2, half_subtractor_1_vem_um;

  half_subtractor half_subtractor_1 (.a(b0), .b(a0), .Resto(Resultado[0]), .Vem_um(half_subtractor_1_vem_um));
  full_subtractor full_subtractor_1 (
    .Vem_um(half_subtractor_1_vem_um), .a(b1), .b(a1), .Resto(Resultado[1]),
    .Vem_um_2(full_subtractor_1_vem_um_2));
  full_subtractor full_subtractor_2 (
    .Vem_um(full_subtractor_1_vem_um_2), .a(b2), .b(a2), .Resto(Resultado[2]), .Vem_um_2(Vem_um));
endmodule

module comparador (
  input  a0,
  input  a1,
  input  a2,
  input  Sinal,
  input  b0,
  input  b1,
  input  b2,
  input  Sinal_2
);

  // NOT_Gate not_1 has open pins: in=a0, out=open
  // NOT_Gate not_2 has open pins: in=a1, out=open
  // NOT_Gate not_3 has open pins: in=a2, out=open
  // NOT_Gate not_4 has open pins: in=Sinal, out=open
  // NOT_Gate not_5 has open pins: in=b0, out=open
  // NOT_Gate not_6 has open pins: in=b1, out=open
  // NOT_Gate not_7 has open pins: in=b2, out=open
  // NOT_Gate not_8 has open pins: in=Sinal_2, out=open
endmodule

module complemento1 (
  input  [2:0] in_1,
  output [2:0] complemento
);

  assign complemento = ~in_1;  // NOT_Gate not_1, 3 bits wide
endmodule

module \and  (
  input  [2:0] in_1,
  output out_2
);

  and and_1 (out_2, in_1[0], in_1[1], in_1[2]);
endmodule

module \or  (
  input  [2:0] in_1,
  output out_2
);

  or or_1 (out_2, in_1[0], in_1[1], in_1[2]);
endmodule
