// Logisim project Guia06.circ as structural Verilog: 11 circuits, main circuit main
module main (
  input  [1:0] Escolha,
  input  [3:0] a,
  input  [3:0] b,
  output Maior,
  output [6:0] OCZ___Num,
  output Diferente
);

  wire adder_4bits_1_carry, adder_4bits_1_ovr, aritmetico_4bits_1_ovr, or_1_out, or_3_out,
       subtractor_4bits_1_carry, subtractor_4bits_1_ovr;
  wire [3:0] \adder_4bits_1_saída , and_1_out, and_2_out, and_3_out, and_4_out, and_5_out, and_6_out,
       and_7_out, and_8_out, and_9_out, and_10_out, and_11_out, and_12_out, or_2_out,
       subtractor_4bits_1_out_4;
  wire [3:3] not_1_out, not_2_out;

  not not_1 (not_1_out[3], Escolha[1]);
  not not_2 (not_2_out[3], Escolha[0]);
  assign and_1_out = {4{not_2_out[3]}} & {4{not_1_out[3]}};  // AND_Gate and_1, 4 bits wide
  assign and_2_out = {4{Escolha[0]}} & {4{not_1_out[3]}};  // AND_Gate and_2, 4 bits wide
  assign and_3_out = {4{not_2_out[3]}} & {4{Escolha[1]}};  // AND_Gate and_3, 4 bits wide
  assign and_4_out = {4{Escolha[0]}} & {4{Escolha[1]}};  // AND_Gate and_4, 4 bits wide
  assign and_5_out = a & and_1_out;  // AND_Gate and_5, 4 bits wide
  assign and_6_out = and_1_out & b;  // AND_Gate and_6, 4 bits wide
  assign and_7_out = a & and_2_out;  // AND_Gate and_7, 4 bits wide
  assign and_8_out = and_2_out & b;  // AND_Gate and_8, 4 bits wide
  assign and_9_out = a & and_3_out;  // AND_Gate and_9, 4 bits wide
  assign and_10_out = and_3_out & b;  // AND_Gate and_10, 4 bits wide
  assign and_11_out = a & and_4_out;  // AND_Gate and_11, 4 bits wide
  assign and_12_out = and_4_out & b;  // AND_Gate and_12, 4 bits wide
  Adder_4bits adder_4bits_1 (
    .a(and_5_out), .b(and_6_out), .Carry(adder_4bits_1_carry), .\Saída (\adder_4bits_1_saída ),
    .Ovr(adder_4bits_1_ovr));
  Subtractor_4bits subtractor_4bits_1 (
    .a(and_7_out), .b(and_8_out), .Carry(subtractor_4bits_1_carry), .out_4(subtractor_4bits_1_out_4),
    .Ovr(subtractor_4bits_1_ovr));
  Comparador_4bits comparador_4bits_1 (.a(and_9_out), .b(and_10_out), .s0(Diferente));
  Aritmetico_4bits aritmetico_4bits_1 (.a(and_11_out), .b(and_12_out), .\Saída (Maior), .Ovr(aritmetico_4bits_1_ovr));
  or or_1 (or_1_out, adder_4bits_1_carry, subtractor_4bits_1_carry);
  assign or_2_out = \adder_4bits_1_saída  | subtractor_4bits_1_out_4;  // OR_Gate or_2, 4 bits wide
  or or_3 (or_3_out, adder_4bits_1_ovr, subtractor_4bits_1_ovr, aritmetico_4bits_1_ovr);
  Final final_1 (.Carry(or_1_out), .Entrada(or_2_out), .a(a), .b(b), .Overflow(or_3_out), .OCZ___Num(OCZ___Num));
endmodule

module Half_Adder (
  input  a,
  input  b,
  output s,
  output c
);

  xor xor_1 (s, a, b);
  and and_1 (c, b, a);
endmodule

module Full_Adder (
  input  a,
  input  b,
  input  c,
  output s,
  output cout
);

  wire half_adder_1_c, half_adder_1_s, half_adder_2_c;

  Half_Adder half_adder_1 (.a(a), .b(b), .s(half_adder_1_s), .c(half_adder_1_c));
  Half_Adder half_adder_2 (.a(half_adder_1_s), .b(c), .s(s), .c(half_adder_2_c));
  or or_1 (cout, half_adder_2_c, half_adder_1_c);
endmodule

module Comparador_4bits (
  input  [3:0] a,
  input  [3:0] b,
  output s0
);

  wire [3:0] xor_1_out;

  assign xor_1_out = a ^ b;  // XOR_Gate xor_1, 4 bits wide
  or or_1 (s0, xor_1_out[0], xor_1_out[1], xor_1_out[2], xor_1_out[3]);

  // Notes on the sheet:
  //   Saída
  //   0 - igual   
  //   1 - diferente
endmodule

module Adder_4bits (
  input  [3:0] a,
  input  [3:0] b,
  output Carry,
  output [3:0] \Saída ,
  output Ovr
);

  wire full_adder_1_cout, full_adder_2_cout, full_adder_3_cout, half_adder_1_c;

  Half_Adder half_adder_1 (.a(a[0]), .b(b[0]), .s(\Saída [0]), .c(half_adder_1_c));
  Full_Adder full_adder_1 (.a(half_adder_1_c), .b(a[1]), .c(b[1]), .s(\Saída [1]), .cout(full_adder_1_cout));
  Full_Adder full_adder_2 (.a(full_adder_1_cout), .b(a[2]), .c(b[2]), .s(\Saída [2]), .cout(full_adder_2_cout));
  Full_Adder full_adder_3 (.a(full_adder_2_cout), .b(a[3]), .c(b[3]), .s(\Saída [3]), .cout(full_adder_3_cout));
  or or_1 (Carry, half_adder_1_c, full_adder_1_cout, full_adder_2_cout, \Saída [3]);
  xor xor_1 (Ovr, full_adder_2_cout, full_adder_3_cout);
endmodule

module Complemento_2 (
  input  [3:0] a,
  output [3:0] Comp_2,
  output Ovr
);

  wire [3:0] not_1_out;

  assign not_1_out = ~a;  // NOT_Gate not_1, 4 bits wide
  Adder_4bits adder_4bits_1 (.a(not_1_out), .b(4'b0001), .\Saída (Comp_2), .Ovr(Ovr));  // open: Carry
endmodule

module Half_Subtractor (
  input  a,
  input  b,
  output s,
  output c
);

  wire not_1_out;

  not not_1 (not_1_out, b);
  xor xor_1 (s, a, b);
  and and_1 (c, not_1_out, a);
endmodule

module Full_Subtractor (
  input  a,
  input  b,
  input  c,
  output s,
  output cout
);

  wire half_subtractor_1_c, half_subtractor_1_s, half_subtractor_2_c;

  Half_Subtractor half_subtractor_1 (.a(a), .b(b), .s(half_subtractor_1_s), .c(half_subtractor_1_c));
  Half_Subtractor half_subtractor_2 (.a(half_subtractor_1_s), .b(c), .s(s), .c(half_subtractor_2_c));
  or or_1 (cout, half_subtractor_1_c, half_subtractor_2_c);
endmodule

module Aritmetico_4bits (
  input  [3:0] a,
  input  [3:0] b,
  output \Saída ,
  output Ovr
);

  wire [2:0] subtractor_4bits_1_out_4;

  Subtractor_4bits subtractor_4bits_1 (
    .a(a), .b(b), .out_4({\Saída , subtractor_4bits_1_out_4}), .Ovr(Ovr));  // open: Carry

  // Notes on the sheet:
  //   Saída
  //   0 - Maior
  //   1 - Menor  
endmodule

module Subtractor_4bits (
  input  [3:0] a,
  input  [3:0] b,
  output Carry,
  output [3:0] out_4,
  output Ovr
);

  wire adder_4bits_1_ovr, complemento_2_1_ovr;
  wire [3:0] complemento_2_1_comp_2;

  Complemento_2 complemento_2_1 (.a(b), .Comp_2(complemento_2_1_comp_2), .Ovr(complemento_2_1_ovr));
  Adder_4bits adder_4bits_1 (
    .a(a), .b(complemento_2_1_comp_2), .Carry(Carry), .\Saída (out_4), .Ovr(adder_4bits_1_ovr));
  xor xor_1 (Ovr, adder_4bits_1_ovr, complemento_2_1_ovr);
endmodule

module Final (
  input  Carry,
  input  [3:0] Entrada,
  input  [3:0] a,
  input  [3:0] b,
  input  Overflow,
  output [6:0] OCZ___Num
);

  wire or_1_out, or_2_out;

  or or_1 (or_1_out, a[0], a[1], a[2], a[3]);
  or or_2 (or_2_out, b[0], b[1], b[2], b[3]);
  nor nor_1 (OCZ___Num[4], or_1_out, or_2_out);

  assign {OCZ___Num[6:5], OCZ___Num[3:0]} = {Overflow, Carry, Entrada};
endmodule
