// Logisim project somador completo.circ as structural Verilog: 1 circuit, main circuit somador completo.circ
module somador_completo_circ (
);

  wire and_1_out, and_2_out, and_3_out, or_1_out, or_2_out, undriven, undriven_2, undriven_3, undriven_4,
       xor_1_out, xor_2_out;

  ExactlyOne xor_1 (.out(xor_1_out), .in0(undriven_4), .in2(undriven_3), .in4(undriven_2));
  and and_1 (and_1_out, undriven_4, undriven_2, undriven_3);
  and and_2 (and_2_out, undriven_4, undriven_3, undriven_2);
  and and_3 (and_3_out, undriven_4, undriven_2);
  xor xor_2 (xor_2_out, xor_1_out, undriven);
  or or_1 (or_1_out, and_1_out, and_2_out);
  or or_2 (or_2_out, or_1_out, and_3_out);

  // Notes on the sheet:
  //   COLOCAR AS ENTRADAS E AS SAIDA TAMBEM
endmodule
