// Logisim project subtrator completo main.circ as structural Verilog: 1 circuit, main circuit subtrator completo main.circ
module subtrator_completo_main_circ (
);

  wire undriven, undriven_2, undriven_3, undriven_4, xor_1_out, xor_2_out, xor_3_out, xor_4_out;
  wire [7:0] subtractor_1_out, subtractor_2_out, subtractor_3_out, subtractor_4_out;

  ExactlyOne xor_1 (.out(xor_1_out), .in1(undriven_4), .in2(undriven_3), .in3(undriven_2), .in4(undriven));
  ExactlyOne xor_2 (.out(xor_2_out), .in0(undriven_4), .in1(undriven_3), .in2(undriven_2), .in3(undriven));
  Subtractor #(.width(8)) subtractor_1 (.out(subtractor_1_out));  // open: a, b, bin, bout
  ExactlyOne xor_3 (.out(xor_3_out), .in0(undriven_4), .in1(undriven_3), .in2(undriven_2), .in4(undriven));
  ExactlyOne xor_4 (.out(xor_4_out), .in1(undriven_4), .in2(undriven_3), .in3(undriven_2), .in4(undriven));
  Subtractor #(.width(8)) subtractor_2 (.out(subtractor_2_out), .bin(xor_2_out));  // open: a, b, bout
  Subtractor #(.width(8)) subtractor_3 (.out(subtractor_3_out));  // open: a, b, bin, bout
  Subtractor #(.width(8)) subtractor_4 (.out(subtractor_4_out), .bin(xor_3_out));  // open: a, b, bout

  // Notes on the sheet:
  //   COLOCAR AS ENTRADAS E AS SAIDAS
endmodule
