// Logisim project exe603.circ as structural Verilog
module meiaSoma (
  input  a,
  input  b,
  output carryOut,
  output soma
);

  and and_1 (carryOut, b, a);
  xor xor_1 (soma, a, b);
endmodule

module somaCompleta (
  input  a,
  input  b,
  input  carryIn,
  output carryOut,
  output s0
);

  wire meiasoma_1_carryout, meiasoma_1_soma, meiasoma_2_carryout;

  or or_1 (carryOut, meiasoma_1_carryout, meiasoma_2_carryout);
  meiaSoma meiasoma_1 (.carryOut(meiasoma_1_carryout), .a(a), .b(b), .soma(meiasoma_1_soma));
  meiaSoma meiasoma_2 (.carryOut(meiasoma_2_carryout), .a(meiasoma_1_soma), .b(carryIn), .soma(s0));
endmodule

module somaAlgebrica__4bits (
  input  [3:0] fator2,
  input  [3:0] fator1,
  input  _0___soma,
  output [3:0] Resultado
);

  wire somacompleta_2_carryout, somacompleta_3_carryout, somacompleta_4_carryout, xor_1_out, xor_2_out,
       xor_3_out, xor_4_out;

  xor xor_1 (xor_1_out, fator2[3], _0___soma);
  somaCompleta somacompleta_1 (
    .a(xor_1_out), .b(fator1[3]), .s0(Resultado[3]), .carryIn(somacompleta_2_carryout));  // open: carryOut
  xor xor_2 (xor_2_out, fator2[2], _0___soma);
  somaCompleta somacompleta_2 (
    .carryOut(somacompleta_2_carryout), .a(xor_2_out), .b(fator1[2]), .s0(Resultado[2]),
    .carryIn(somacompleta_3_carryout));
  xor xor_3 (xor_3_out, fator2[1], _0___soma);
  somaCompleta somacompleta_3 (
    .carryOut(somacompleta_3_carryout), .a(xor_3_out), .b(fator1[1]), .s0(Resultado[1]),
    .carryIn(somacompleta_4_carryout));
  xor xor_4 (xor_4_out, fator2[0], _0___soma);
  somaCompleta somacompleta_4 (
    .carryOut(somacompleta_4_carryout), .a(xor_4_out), .b(fator1[0]), .s0(Resultado[0]), .carryIn(_0___soma));

  // Notes on the sheet:
  //   1 - subtrai
endmodule

module comparador__4bits (
  input  [3:0] in_1,
  input  [3:0] in_2,
  output out_3
);

  wire [3:0] xnor_1_out;

  assign xnor_1_out = ~(in_1 ^ in_2);  // XNOR_Gate xnor_1, 4 bits wide
  and and_1 (out_3, xnor_1_out[3], xnor_1_out[2], xnor_1_out[1], xnor_1_out[0]);

  // Notes on the sheet:
  //   Comparador Aritimetico
endmodule

module ULA (
  input  [3:0] fator1,
  input  [3:0] fator2,
  input  in_3,
  output [3:0] Resultado,
  output overflow,
  output menor,
  output maior,
  output igual
);

  Comparador_Aritmetico comparador_aritmetico_1 (
    .fator1(fator1), .fator2(fator2), .menor(menor), .maior(maior), .igual(igual));
  somaAlgebrica__4bits somaalgebrica_4bits_1 (
    .fator2(fator2), .fator1(fator1), .Resultado(Resultado), ._0___soma(in_3));
  overflow overflow_1 (.am(fator1), .bm(fator2), .op(in_3), .sm(Resultado), .overflow(overflow));
endmodule

module Comparador_Aritmetico (
  input  [3:0] fator1,
  input  [3:0] fator2,
  output menor,
  output maior,
  output igual
);

  wire [2:0] somaalgebrica_4bits_1_resultado;

  somaAlgebrica__4bits somaalgebrica_4bits_1 (
    .fator2(fator2), .fator1(fator1), .Resultado({menor, somaalgebrica_4bits_1_resultado}), ._0___soma(1'b1));
  comparador__4bits comparador_4bits_1 (.in_1(fator1), .in_2(fator2), .out_3(igual));
  nor nor_1 (maior, menor, igual);

  // Notes on the sheet:
  //   Comparador Aritimético
endmodule

module overflow (
  input  [3:0] am,
  input  [3:0] bm,
  input  op,
  input  [3:0] sm,
  output overflow
);

  wire and_1_out, and_2_out, not_1_out, not_2_out, not_3_out;

  not not_1 (not_1_out, am[3]);
  not not_2 (not_2_out, bm[3]);
  not not_3 (not_3_out, op);
  and and_1 (and_1_out, not_1_out, not_2_out, not_3_out);
  and and_2 (and_2_out, op, bm[3], sm[3]);
  or or_1 (overflow, and_1_out, and_2_out);
endmodule

module zero (
  input  [3:0] fator,
  input  [3:0] in_2,
  output out_3
);

  comparador__4bits comparador_4bits_1 (.in_1(fator), .in_2(in_2), .out_3(out_3));
endmodule
