// Logisim project exe604.circ as structural Verilog: 10 circuits, main circuit meiaSoma
module meiaSoma (
  input  a,
  input  b,
  output carryOut,
  output soma
);

  and and_1 (carryOut, b, a);
  xor xor_1 (soma, a, b);
endmodule

module somaCompleta (
  input  a,
  input  b,
  input  carryIn,
  output carryOut,
  output s0
);

  wire meiasoma_1_carryout, meiasoma_1_soma, meiasoma_2_carryout;

  or or_1 (carryOut, meiasoma_1_carryout, meiasoma_2_carryout);
  meiaSoma meiasoma_1 (.carryOut(meiasoma_1_carryout), .a(a), .b(b), .soma(meiasoma_1_soma));
  meiaSoma meiasoma_2 (.carryOut(meiasoma_2_carryout), .a(meiasoma_1_soma), .b(carryIn), .soma(s0));
endmodule

module somaAlgebrica__4bits (
  input  [3:0] fator2,
  input  [3:0] fator1,
  input  in_3,
  output CarryOut,
  output [3:0] Resultado
);

  wire somacompleta_2_carryout, somacompleta_3_carryout, somacompleta_4_carryout;
  wire [3:0] complemento_de_1_1_complemento_1;

  somaCompleta somacompleta_1 (
    .carryOut(CarryOut), .a(fator1[3]), .b(complemento_de_1_1_complemento_1[3]), .s0(Resultado[3]),
    .carryIn(somacompleta_2_carryout));
  somaCompleta somacompleta_2 (
    .carryOut(somacompleta_2_carryout), .a(fator1[2]), .b(complemento_de_1_1_complemento_1[2]),
    .s0(Resultado[2]), .carryIn(somacompleta_3_carryout));
  somaCompleta somacompleta_3 (
    .carryOut(somacompleta_3_carryout), .a(fator1[1]), .b(complemento_de_1_1_complemento_1[1]),
    .s0(Resultado[1]), .carryIn(somacompleta_4_carryout));
  complemento_de_1 complemento_de_1_1 (.fator(fator2), .Complemento_1(complemento_de_1_1_complemento_1));
  somaCompleta somacompleta_4 (
    .carryOut(somacompleta_4_carryout), .a(fator1[0]), .b(complemento_de_1_1_complemento_1[0]),
    .s0(Resultado[0]), .carryIn(in_3));
endmodule

module comparador__4bits (
  input  [3:0] in_1,
  input  [3:0] in_2,
  output out_3
);

  wire [3:0] xnor_1_out;

  assign xnor_1_out = ~(in_1 ^ in_2);  // XNOR_Gate xnor_1, 4 bits wide
  and and_1 (out_3, xnor_1_out[3], xnor_1_out[2], xnor_1_out[1], xnor_1_out[0]);

  // Notes on the sheet:
  //   Comparador Aritimetico
endmodule

module ULA (
  input  [3:0] fator1,
  input  [3:0] fator2,
  input  in_3,
  input  [3:0] in_4,
  output [3:0] out_5,
  output [3:0] out_6,
  output [3:0] Resultado,
  output overflow,
  output menor,
  output maior,
  output igual,
  output zero,
  output carry
);

  Comparador_Aritmetico comparador_aritmetico_1 (
    .fator1(fator1), .fator2(fator2), .menor(menor), .maior(maior), .igual(igual));
  somaAlgebrica__4bits somaalgebrica_4bits_1 (
    .CarryOut(carry), .fator1(fator2), .fator2(fator1), .Resultado(Resultado), .in_3(in_3));
  complemento_de_1 complemento_de_1_1 (.fator(fator1), .Complemento_1(out_5));
  complemento_de_1 complemento_de_1_2 (.fator(fator2), .Complemento_1(out_6));
  overflow overflow_1 (.am(fator1), .bm(fator2), .op(in_3), .sm(Resultado), .overflow(overflow));
  zero zero_1 (.fator(in_4), .in_2(Resultado), .out_3(zero));
endmodule

module Comparador_Aritmetico (
  input  [3:0] fator1,
  input  [3:0] fator2,
  output menor,
  output maior,
  output igual
);

  wire [2:0] somaalgebrica_4bits_1_resultado;

  somaAlgebrica__4bits somaalgebrica_4bits_1 (
    .fator1(fator2), .fator2(fator1), .Resultado({menor, somaalgebrica_4bits_1_resultado}), .in_3(1'b1));  // open: CarryOut
  comparador__4bits comparador_4bits_1 (.in_1(fator1), .in_2(fator2), .out_3(igual));
  nor nor_1 (maior, menor, igual);

  // Notes on the sheet:
  //   Comparador Aritimético
endmodule

module overflow (
  input  [3:0] am,
  input  [3:0] bm,
  input  op,
  input  [3:0] sm,
  output overflow
);

  wire and_1_out, not_1_out, xnor_1_out;

  xnor xnor_1 (xnor_1_out, bm[3], op);
  not not_1 (not_1_out, am[3]);
  and and_1 (and_1_out, not_1_out, sm[3]);
  and and_2 (overflow, xnor_1_out, and_1_out);

  // Notes on the sheet:
  //   Overflow
endmodule

module zero (
  input  [3:0] fator,
  input  [3:0] in_2,
  output out_3
);

  comparador__4bits comparador_4bits_1 (.in_1(fator), .in_2(in_2), .out_3(out_3));
endmodule

module carry (
  input  [3:0] fator,
  input  [3:0] in_2,
  input  op,
  output carryOut
);

  somaAlgebrica__4bits somaalgebrica_4bits_1 (
    .CarryOut(carryOut), .fator1(fator), .fator2(in_2), .in_3(op));  // open: Resultado
endmodule

module complemento_de_1 (
  input  [3:0] fator,
  output [3:0] Complemento_1
);

  assign Complemento_1 = ~fator;  // NOT_Gate not_1, 4 bits wide

  // Notes on the sheet:
  //   Complemento de 1
endmodule
