// Logisim project Guia06.circ as structural Verilog: 4 circuits, main circuit ALU
module ALU (
  input  Sub,
  input  a0,
  input  b0,
  input  a1,
  input  b1,
  input  a2,
  input  b2,
  input  a3,
  input  b3,
  output s0,
  output s1,
  output s2,
  output s3,
  output s4,
  output Diferente,
  output Igual,
  output A_B,
  output A_B_2,
  output Carry,
  output Overflow,
  output Zero
);

  wire full_adder_1_s1, full_adder_2_s1, full_adder_3_s1, not_1_out, xor_1_out, xor_2_out, xor_3_out,
       xor_4_out;

  xor xor_1 (xor_1_out, b0, Sub);
  xor xor_2 (xor_2_out, b1, Sub);
  xor xor_3 (xor_3_out, b2, Sub);
  xor xor_4 (xor_4_out, b3, Sub);
  comparador comparador_1 (
    .a0(a0), .b0(b0), .a1(a1), .b1(b1), .a2(a2), .b2(b2), .a3(a3), .b3(b3), .A_B(A_B_2), .A_B_2(A_B),
    .Igual(Igual), .Diferente(Diferente));
  full_adder full_adder_1 (.A(a0), .B(xor_1_out), .Cin(Sub), .s0(s0), .s1(full_adder_1_s1));
  full_adder full_adder_2 (.A(a1), .B(xor_2_out), .Cin(full_adder_1_s1), .s0(s1), .s1(full_adder_2_s1));
  full_adder full_adder_3 (.A(a2), .B(xor_3_out), .Cin(full_adder_2_s1), .s0(s2), .s1(full_adder_3_s1));
  full_adder full_adder_4 (.A(a3), .B(xor_4_out), .Cin(full_adder_3_s1), .s0(s3), .s1(Carry));
  not not_1 (not_1_out, full_adder_3_s1);
  and and_1 (Overflow, Carry, not_1_out);
  nor nor_1 (Zero, s0, s1, s2, s3, s4);
  xor xor_5 (s4, Carry, Sub);
endmodule

module half_adder (
  input  A,
  input  B,
  output s0,
  output s1
);

  wire not_1_out, or_1_out;

  or or_1 (or_1_out, A, B);
  and and_1 (s1, A, B);
  not not_1 (not_1_out, s1);
  and and_2 (s0, or_1_out, or_1_out, not_1_out);
endmodule

module full_adder (
  input  A,
  input  B,
  input  Cin,
  output s0,
  output s1
);

  wire half_adder_1_s0, half_adder_1_s1, half_adder_2_s1;

  half_adder half_adder_1 (.A(A), .B(B), .s0(half_adder_1_s0), .s1(half_adder_1_s1));
  half_adder half_adder_2 (.A(half_adder_1_s0), .B(Cin), .s0(s0), .s1(half_adder_2_s1));
  or or_1 (s1, half_adder_2_s1, half_adder_1_s1);
endmodule

module comparador (
  input  a0,
  input  b0,
  input  a1,
  input  b1,
  input  a2,
  input  b2,
  input  a3,
  input  b3,
  output A_B,
  output A_B_2,
  output Igual,
  output Diferente
);

  wire and_1_out, and_2_out, and_3_out, and_4_out, and_5_out, and_6_out, and_7_out, and_8_out, and_9_out,
       and_10_out, and_11_out, and_12_out, and_13_out, and_14_out, nor_1_out, nor_2_out, nor_3_out,
       nor_4_out, not_1_out, not_2_out, not_3_out, not_4_out, not_5_out, not_6_out, not_7_out, not_8_out;

  not not_1 (not_1_out, a0);
  not not_2 (not_2_out, b0);
  not not_3 (not_3_out, a1);
  not not_4 (not_4_out, b1);
  not not_5 (not_5_out, a2);
  not not_6 (not_6_out, b2);
  not not_7 (not_7_out, a3);
  not not_8 (not_8_out, b3);
  and and_1 (and_1_out, not_1_out, b0);
  and and_2 (and_2_out, a0, not_2_out);
  and and_3 (and_3_out, not_3_out, b1);
  and and_4 (and_4_out, a1, not_4_out);
  and and_5 (and_5_out, not_5_out, b2);
  and and_6 (and_6_out, a2, not_6_out);
  and and_7 (and_7_out, not_7_out, b3);
  and and_8 (and_8_out, a3, not_8_out);
  nor nor_1 (nor_1_out, and_1_out, and_2_out);
  nor nor_2 (nor_2_out, and_3_out, and_4_out);
  nor nor_3 (nor_3_out, and_5_out, and_6_out);
  nor nor_4 (nor_4_out, and_7_out, and_8_out);
  and and_9 (and_9_out, and_3_out, nor_1_out);
  and and_10 (and_10_out, and_4_out, nor_1_out);
  and and_11 (and_11_out, and_5_out, nor_1_out, nor_2_out);
  and and_12 (and_12_out, and_6_out, nor_1_out, nor_2_out);
  and and_13 (and_13_out, and_7_out, nor_1_out, nor_2_out, nor_3_out);
  and and_14 (and_14_out, nor_1_out, nor_2_out, and_8_out, nor_3_out);
  and and_15 (Igual, nor_1_out, nor_2_out, nor_3_out, nor_4_out);
  or or_1 (A_B, and_1_out, and_9_out, and_13_out, and_11_out);
  or or_2 (A_B_2, and_2_out, and_10_out, and_12_out, and_14_out);
  not not_9 (Diferente, Igual);
endmodule
