// Logisim project guia_06.circ as structural Verilog: 12 circuits, main circuit main
module main (
  input  a0,
  input  a1,
  input  a2,
  input  a3,
  input  b0,
  input  b1,
  input  b2,
  input  b3,
  input  op,
  output s0,
  output s1,
  output s2,
  output s3,
  output s4,
  output out_15,
  output s0_2,
  output s1_2,
  output s2_2,
  output s3_2,
  output s4_2,
  output a_b,
  output a_b_2,
  output zero,
  output carry,
  output overflow
);

  ex_01 ex_01_1 (
    .a0(a0), .a1(a1), .a2(a2), .a3(a3), .b0(b0), .b1(b1), .b2(b2), .b3(b3), .op(op), .s0(s0), .s1(s1),
    .s2(s2), .s3(s3), .s4(s4), .out_15(out_15));
  ex_02 ex_02_1 (
    .a0(a0), .a1(a1), .a2(a2), .a3(a3), .b0(b1), .b1(b3), .b2(b3), .b3(op), .s0(s0_2), .s1(s1_2), .s2(s2_2),
    .s3(s3_2), .s0_2(s4_2), .a_b(a_b), .a_b_2(a_b_2));
  ex_03 ex_03_1 (
    .a0(a0), .a1(a1), .a2(a2), .a3(a3), .b0(b1), .b1(b3), .b2(b3), .b3(op), .zero(zero), .carry(carry),
    .overflow(overflow));

  // Notes on the sheet:
  //   0 - diferente
  //   1 - igual
endmodule

module half_adder (
  input  x,
  input  y,
  output s0,
  output s1
);

  xor xor_1 (s0, x, y);
  and and_1 (s1, x, y);
endmodule

module full_adder (
  input  v_in,
  input  x,
  input  y,
  output s0,
  output s1
);

  wire half_adder_1_s0, half_adder_1_s1, half_adder_2_s1;

  half_adder half_adder_1 (.x(x), .y(y), .s0(half_adder_1_s0), .s1(half_adder_1_s1));
  half_adder half_adder_2 (.x(v_in), .y(half_adder_1_s0), .s0(s0), .s1(half_adder_2_s1));
  or or_1 (s1, half_adder_2_s1, half_adder_1_s1);
endmodule

module equal_comp (
  input  a0,
  input  a1,
  input  a2,
  input  a3,
  input  b0,
  input  b1,
  input  b2,
  input  b3,
  input  op,
  output out_10
);

  wire and_1_out, and_2_out, not_1_out, not_2_out, or_1_out, xor_1_out, xor_2_out, xor_3_out, xor_4_out;

  xor xor_1 (xor_1_out, a0, b0);
  xor xor_2 (xor_2_out, a1, b1);
  xor xor_3 (xor_3_out, a2, b2);
  xor xor_4 (xor_4_out, a3, b3);
  or or_1 (or_1_out, xor_1_out, xor_2_out, xor_3_out, xor_4_out);
  not not_1 (not_1_out, or_1_out);
  not not_2 (not_2_out, op);
  and and_1 (and_1_out, or_1_out, not_2_out);
  and and_2 (and_2_out, op, not_1_out);
  or or_2 (out_10, and_1_out, and_2_out);

  // Notes on the sheet:
  //   0 - diferente
  //   1 - igual
endmodule

module ex_01 (
  input  a0,
  input  a1,
  input  a2,
  input  a3,
  input  b0,
  input  b1,
  input  b2,
  input  b3,
  input  op,
  output s0,
  output s1,
  output s2,
  output s3,
  output s4,
  output out_15
);

  wire full_adder_1_s1, full_adder_2_s1, half_adder_1_s1;

  equal_comp equal_comp_1 (
    .a0(a0), .a1(a1), .a2(a2), .a3(a3), .b0(b0), .b1(b1), .b2(b2), .b3(b3), .op(op), .out_10(out_15));
  half_adder half_adder_1 (.x(a0), .y(b0), .s0(s0), .s1(half_adder_1_s1));
  full_adder full_adder_1 (.v_in(half_adder_1_s1), .x(a1), .y(b1), .s0(s1), .s1(full_adder_1_s1));
  full_adder full_adder_2 (.v_in(full_adder_1_s1), .x(a2), .y(b2), .s0(s2), .s1(full_adder_2_s1));
  full_adder full_adder_3 (.v_in(full_adder_2_s1), .x(a3), .y(b3), .s0(s3), .s1(s4));

  // Notes on the sheet:
  //   0 - diferente
  //   1 - igual
endmodule

module carry_over (
  input  a0,
  input  a1,
  input  a2,
  input  a3,
  input  b0,
  input  b1,
  input  b2,
  input  b3,
  output carry,
  output overflow
);

  wire full_adder_1_s1, full_adder_2_s0, full_adder_2_s1, full_adder_3_s1, half_adder_1_s1, not_1_out;

  half_adder half_adder_1 (.x(a0), .y(b0), .s1(half_adder_1_s1));  // open: s0
  full_adder full_adder_1 (.v_in(half_adder_1_s1), .x(a1), .y(b1), .s1(full_adder_1_s1));  // open: s0
  full_adder full_adder_2 (.v_in(full_adder_1_s1), .x(a2), .y(b2), .s0(full_adder_2_s0), .s1(full_adder_2_s1));
  full_adder full_adder_3 (.v_in(full_adder_2_s1), .x(a3), .y(b3), .s1(full_adder_3_s1));  // open: s0
  not not_1 (not_1_out, full_adder_2_s0);
  or or_1 (carry, half_adder_1_s1, full_adder_1_s1, full_adder_2_s1, full_adder_3_s1);
  and and_1 (overflow, not_1_out, full_adder_3_s1);
endmodule

module zero (
  input  s0,
  input  s1,
  input  s2,
  input  s3,
  output zero
);

  nor nor_1 (zero, s0, s1, s2, s3);
endmodule

module ex_03 (
  input  a0,
  input  a1,
  input  a2,
  input  a3,
  input  b0,
  input  b1,
  input  b2,
  input  b3,
  output zero,
  output carry,
  output overflow
);

  wire zero_1_zero, zero_2_zero;

  zero zero_1 (.s0(a0), .s1(a1), .s2(a2), .s3(a3), .zero(zero_1_zero));
  zero zero_2 (.s0(b0), .s1(b1), .s2(b2), .s3(b3), .zero(zero_2_zero));
  carry_over carry_over_1 (
    .a0(a0), .a1(a1), .a2(a2), .a3(a3), .b0(b0), .b1(b1), .b2(b2), .b3(b3), .carry(carry), .overflow(overflow));
  and and_1 (zero, zero_1_zero, zero_2_zero);
endmodule

module half_sub (
  input  y,
  input  x,
  output s0,
  output b_out
);

  wire not_1_out;

  not not_1 (not_1_out, x);
  xor xor_1 (s0, y, x);
  and and_1 (b_out, not_1_out, y);
endmodule

module full_sub (
  input  borrow_in,
  input  y,
  input  x,
  output s0,
  output s1
);

  wire half_sub_1_b_out, half_sub_1_s0, half_sub_2_b_out;

  half_sub half_sub_1 (.y(y), .x(x), .s0(half_sub_1_s0), .b_out(half_sub_1_b_out));
  half_sub half_sub_2 (.y(borrow_in), .x(half_sub_1_s0), .s0(s0), .b_out(half_sub_2_b_out));
  or or_1 (s1, half_sub_2_b_out, half_sub_1_b_out);
endmodule

module comp (
  input  a0,
  input  a1,
  input  a2,
  input  a3,
  input  b0,
  input  b1,
  input  b2,
  input  b3,
  output a_b,
  output a_b_2,
  output a_b_3,
  output a__b
);

  wire and_1_out, and_2_out, and_3_out, and_4_out, and_5_out, and_6_out, and_7_out, and_8_out, and_9_out,
       and_10_out, and_11_out, and_12_out, and_13_out, and_14_out, nor_1_out, nor_2_out, nor_3_out,
       nor_4_out, not_1_out, not_2_out, not_3_out, not_4_out, not_5_out, not_6_out, not_7_out, not_8_out;

  not not_1 (not_1_out, a0);
  not not_2 (not_2_out, b0);
  not not_3 (not_3_out, a1);
  not not_4 (not_4_out, b1);
  not not_5 (not_5_out, a2);
  not not_6 (not_6_out, b2);
  not not_7 (not_7_out, a3);
  not not_8 (not_8_out, b3);
  and and_1 (and_1_out, not_1_out, b0);
  and and_2 (and_2_out, a0, not_2_out);
  and and_3 (and_3_out, not_3_out, b1);
  and and_4 (and_4_out, a1, not_4_out);
  and and_5 (and_5_out, not_5_out, b2);
  and and_6 (and_6_out, a2, not_6_out);
  and and_7 (and_7_out, not_7_out, b3);
  and and_8 (and_8_out, a3, not_8_out);
  nor nor_1 (nor_1_out, and_1_out, and_2_out);
  nor nor_2 (nor_2_out, and_3_out, and_4_out);
  nor nor_3 (nor_3_out, and_5_out, and_6_out);
  nor nor_4 (nor_4_out, and_7_out, and_8_out);
  and and_9 (and_9_out, nor_1_out, and_3_out);
  and and_10 (and_10_out, nor_1_out, and_4_out);
  and and_11 (and_11_out, nor_1_out, and_5_out, nor_2_out);
  and and_12 (and_12_out, nor_1_out, and_6_out, nor_2_out);
  and and_13 (and_13_out, nor_1_out, and_7_out, nor_2_out, nor_3_out);
  and and_14 (and_14_out, nor_1_out, and_8_out, nor_2_out, nor_3_out);
  and and_15 (a_b_3, nor_1_out, nor_2_out, nor_3_out, nor_4_out);
  or or_1 (a_b, and_1_out, and_9_out, and_11_out, and_13_out);
  or or_2 (a_b_2, and_2_out, and_10_out, and_12_out, and_14_out);
  not not_9 (a__b, a_b_3);
endmodule

module ex_02 (
  input  a0,
  input  a1,
  input  a2,
  input  a3,
  input  b0,
  input  b1,
  input  b2,
  input  b3,
  output s0,
  output s1,
  output s2,
  output s3,
  output s0_2,
  output a_b,
  output a_b_2
);

  wire full_sub_1_s1, full_sub_2_s1, half_sub_1_b_out;

  half_sub half_sub_1 (.y(b0), .x(a0), .s0(s0), .b_out(half_sub_1_b_out));
  full_sub full_sub_1 (.borrow_in(half_sub_1_b_out), .y(b1), .x(a1), .s0(s1), .s1(full_sub_1_s1));
  comp comp_1 (
    .a0(a0), .a1(a1), .a2(a2), .a3(a3), .b0(b0), .b1(b1), .b2(b2), .b3(b3), .a_b(a_b), .a_b_2(a_b_2));  // open: a_b_3, a__b
  full_sub full_sub_2 (.borrow_in(full_sub_1_s1), .y(b2), .x(a2), .s0(s2), .s1(full_sub_2_s1));
  full_sub full_sub_3 (.borrow_in(full_sub_2_s1), .y(a3), .x(b3), .s0(s3), .s1(s0_2));
endmodule
