// Logisim project ALU_4BITS.circ as structural Verilog: 10 circuits, main circuit half_adder
module main (
  input  a3,
  input  a2,
  input  a1,
  input  a0,
  input  b3,
  input  b2,
  input  b1,
  input  b0,
  output DIFERENCA,
  output A___B,
  output CARRY,
  output OVERFLOW,
  output ZERO,
  output sS3,
  output sS2,
  output sS1,
  output sS0,
  output a_prime_3,
  output a_prime_2,
  output a_prime_1,
  output a_prime_0,
  output b_prime_3,
  output b_prime_2,
  output b_prime_1,
  output b_prime_0,
  output s3,
  output s2,
  output s1,
  output s0
);

  ALU_4bits alu_4bits_1 (
    .a3(a3), .a2(a2), .a1(a1), .a0(a0), .b3(b3), .b2(b2), .b1(b1), .b0(b0), ._1__a_maior___0__a_menor(A___B),
    .a_prime_3(a_prime_3), .b_prime_3(b_prime_3), .a_prime_2(a_prime_2), .b_prime_2(b_prime_2),
    .a_prime_1(a_prime_1), .b_prime_1(b_prime_1), .s3(s3), .a_prime_0(a_prime_0), .b_prime_0(b_prime_0),
    .s2(s2), .s1(s1), .sS3(sS3), .s0(s0), .sS2(sS2), .sS1(sS1), .sS0(sS0), .ZERO(ZERO), .OVERFLOW(OVERFLOW),
    .CARRY(CARRY), .DIFERENTE(DIFERENCA));

  // Notes on the sheet:
  //   complemento de a
  //   complemento de b
  //   soma
  //   subtração
endmodule

module half_adder (
  input  A,
  input  B,
  output S0,
  output S1
);

  xor xor_1 (S0, A, B);
  and and_1 (S1, A, B);
endmodule

module full_adder (
  input  A,
  input  B,
  input  C,
  output S0,
  output S1
);

  wire half_adder_1_s0, half_adder_1_s1, half_adder_2_s1;

  half_adder half_adder_1 (.A(A), .B(B), .S0(half_adder_1_s0), .S1(half_adder_1_s1));
  half_adder half_adder_2 (.A(half_adder_1_s0), .B(C), .S0(S0), .S1(half_adder_2_s1));
  or or_1 (S1, half_adder_2_s1, half_adder_1_s1);

  // Notes on the sheet:
  //   meia-soma
  //   meia-soma
endmodule

module haf_subtractor (
  input  A,
  input  B,
  output S0,
  output S1
);

  wire and_1_out, and_2_out, not_1_out, not_2_out, not_3_out;

  not not_1 (not_1_out, A);
  not not_2 (not_2_out, B);
  not not_3 (not_3_out, A);
  and and_1 (and_1_out, not_1_out, B);
  and and_2 (and_2_out, A, not_2_out);
  and and_3 (S1, not_3_out, B);
  or or_1 (S0, and_1_out, and_2_out);
endmodule

module full_subtractor (
  input  A,
  input  B,
  input  C,
  output S0,
  output S1
);

  wire haf_subtractor_1_s0, haf_subtractor_1_s1, haf_subtractor_2_s1;

  haf_subtractor haf_subtractor_1 (.A(A), .B(B), .S0(haf_subtractor_1_s0), .S1(haf_subtractor_1_s1));
  haf_subtractor haf_subtractor_2 (.A(haf_subtractor_1_s0), .B(C), .S0(S0), .S1(haf_subtractor_2_s1));
  or or_1 (S1, haf_subtractor_2_s1, haf_subtractor_1_s1);
endmodule

module Somador_4bits (
  input  a3,
  input  a2,
  input  a1,
  input  a0,
  input  b3,
  input  b2,
  input  b1,
  input  b0,
  output s4,
  output s3,
  output s2,
  output s1,
  output s0,
  output aux_overflow
);

  wire full_adder_1_s1, full_adder_2_s1, full_adder_3_s1;

  full_adder full_adder_1 (.A(a0), .B(b0), .C(1'b0), .S0(s0), .S1(full_adder_1_s1));
  full_adder full_adder_2 (.A(a1), .B(b1), .C(full_adder_1_s1), .S0(s1), .S1(full_adder_2_s1));
  full_adder full_adder_3 (.A(a2), .B(b2), .C(full_adder_2_s1), .S0(s2), .S1(full_adder_3_s1));
  full_adder full_adder_4 (.A(a3), .B(b3), .C(full_adder_3_s1), .S0(s3), .S1(s4));
  not not_1 (aux_overflow, full_adder_3_s1);

  // Notes on the sheet:
  //   A + B
  //   full-adder
  //   full-adder
  //   full-adder
endmodule

module Subtrator_4bits (
  input  a3,
  input  a2,
  input  a1,
  input  a0,
  input  b3,
  input  b2,
  input  b1,
  input  b0,
  output s3,
  output s2,
  output s1,
  output s0,
  output comparador
);

  wire full_subtractor_1_s1, full_subtractor_2_s1, full_subtractor_3_s1;

  full_subtractor full_subtractor_1 (.A(a0), .B(b0), .C(1'b0), .S0(s0), .S1(full_subtractor_1_s1));
  full_subtractor full_subtractor_2 (.A(a1), .B(b1), .C(full_subtractor_1_s1), .S0(s1), .S1(full_subtractor_2_s1));
  full_subtractor full_subtractor_3 (.A(a2), .B(b2), .C(full_subtractor_2_s1), .S0(s2), .S1(full_subtractor_3_s1));
  full_subtractor full_subtractor_4 (.A(a3), .B(b3), .C(full_subtractor_3_s1), .S0(s3), .S1(comparador));

  // Notes on the sheet:
  //   A - B
  //   full-subtractor
  //   full-subtractor
  //   1: a é maior
  //   0: a é menor
endmodule

module Comparador_logico_4bits (
  input  a3,
  input  a2,
  input  a1,
  input  a0,
  input  b3,
  input  b2,
  input  b1,
  input  b0,
  output s
);

  wire xor_1_out, xor_2_out, xor_3_out, xor_4_out;

  xor xor_1 (xor_1_out, b0, a0);
  xor xor_2 (xor_2_out, b1, a1);
  xor xor_3 (xor_3_out, b2, a2);
  xor xor_4 (xor_4_out, b3, a3);
  or or_1 (s, xor_1_out, xor_2_out, xor_3_out, xor_4_out);

  // Notes on the sheet:
  //   0: é igual
  //   1: é diferente
endmodule

module complemento_de_um (
  input  a3,
  input  a2,
  input  a1,
  input  a0,
  output s3,
  output s2,
  output s1,
  output s0
);

  not not_1 (s0, a0);
  not not_2 (s1, a1);
  not not_3 (s2, a2);
  not not_4 (s3, a3);
endmodule

module ALU_4bits (
  input  a3,
  input  a2,
  input  a1,
  input  a0,
  input  b3,
  input  b2,
  input  b1,
  input  b0,
  output s3,
  output s2,
  output s1,
  output s0,
  output ZERO,
  output OVERFLOW,
  output CARRY,
  output DIFERENTE,
  output a_prime_3,
  output a_prime_2,
  output a_prime_1,
  output a_prime_0,
  output b_prime_3,
  output b_prime_2,
  output b_prime_1,
  output b_prime_0,
  output sS3,
  output sS2,
  output sS1,
  output sS0,
  output _1__a_maior___0__a_menor
);

  wire somador_4bits_1_aux_overflow;

  Somador_4bits somador_4bits_1 (
    .a3(a3), .a2(a2), .a1(a1), .a0(a0), .b3(b3), .b2(b2), .b1(b1), .b0(b0), .s4(CARRY), .s3(s3), .s2(s2),
    .s1(s1), .s0(s0), .aux_overflow(somador_4bits_1_aux_overflow));
  Comparador_logico_4bits comparador_logico_4bits_1 (
    .a3(a3), .a2(a2), .a1(a1), .a0(a0), .b3(b3), .b2(b2), .b1(b1), .b0(b0), .s(DIFERENTE));
  complemento_de_um complemento_de_um_1 (
    .a3(a3), .a2(a2), .a1(a1), .a0(a0), .s3(a_prime_3), .s2(a_prime_2), .s1(a_prime_1), .s0(a_prime_0));
  complemento_de_um complemento_de_um_2 (
    .a3(b3), .a2(b2), .a1(b1), .a0(b0), .s3(b_prime_3), .s2(b_prime_2), .s1(b_prime_1), .s0(b_prime_0));
  Subtrator_4bits subtrator_4bits_1 (
    .a3(a3), .a2(a2), .a1(a1), .a0(a0), .b3(b3), .b2(b2), .b1(b1), .b0(b0), .s3(sS3), .s2(sS2), .s1(sS1),
    .s0(sS0), .comparador(_1__a_maior___0__a_menor));
  and and_1 (OVERFLOW, somador_4bits_1_aux_overflow, CARRY);
  nor nor_1 (ZERO, a3, a2, a1, a0, b3, b2, b1, b0);

  // Notes on the sheet:
  //   comparador logico
  //   somador_4bits - indicador de overflow e indicador de carry
  //   comparador lógico
  //   A
  //   B
  //   complementos de 1
  //   a - b
endmodule
