// Logisim project Exercicio01.circ as structural Verilog: 5 circuits, main circuit meia soma
module meia_soma (
  input  in_1,
  input  in_2,
  output out_3,
  output out_4
);

  xor xor_1 (out_3, in_1, in_2);
  and and_1 (out_4, in_1, in_2);
endmodule

module soma_completa (
  input  in_1,
  input  in_2,
  input  in_3,
  output out_4,
  output out_5
);

  wire meia_soma_1_out_3, meia_soma_1_out_4, meia_soma_2_out_4;

  meia_soma meia_soma_1 (.in_1(in_1), .in_2(in_2), .out_3(meia_soma_1_out_3), .out_4(meia_soma_1_out_4));
  meia_soma meia_soma_2 (.in_1(meia_soma_1_out_3), .in_2(in_3), .out_3(out_4), .out_4(meia_soma_2_out_4));
  or or_1 (out_5, meia_soma_2_out_4, meia_soma_1_out_4);
endmodule

module Soma_4_btis (
  input  [3:0] in_1,
  input  [3:0] in_2,
  output [4:0] out_3
);

  wire meia_soma_1_out_4, soma_completa_1_out_5, soma_completa_2_out_5;

  meia_soma meia_soma_1 (.in_1(in_1[0]), .in_2(in_2[0]), .out_3(out_3[0]), .out_4(meia_soma_1_out_4));
  soma_completa soma_completa_1 (
    .in_1(meia_soma_1_out_4), .in_2(in_1[1]), .in_3(in_2[1]), .out_4(out_3[1]), .out_5(soma_completa_1_out_5));
  soma_completa soma_completa_2 (
    .in_1(soma_completa_1_out_5), .in_2(in_1[2]), .in_3(in_2[2]), .out_4(out_3[2]),
    .out_5(soma_completa_2_out_5));
  soma_completa soma_completa_3 (
    .in_1(soma_completa_2_out_5), .in_2(in_1[3]), .in_3(in_2[3]), .out_4(out_3[3]), .out_5(out_3[4]));
endmodule

module comparador (
  input  [3:0] in_1,
  input  [3:0] in_2,
  output out_3
);

  wire or_1_out, or_2_out, xor_1_out, xor_2_out, xor_3_out, xor_4_out;

  xor xor_1 (xor_1_out, in_1[0], in_2[0]);
  xor xor_2 (xor_2_out, in_1[1], in_2[1]);
  xor xor_3 (xor_3_out, in_1[2], in_2[2]);
  xor xor_4 (xor_4_out, in_1[3], in_2[3]);
  or or_1 (or_1_out, xor_1_out, xor_2_out);
  or or_2 (or_2_out, xor_3_out, xor_4_out);
  or or_3 (out_3, or_1_out, or_2_out);
endmodule

module main (
  input  [3:0] a,
  input  [3:0] b,
  output [4:0] soma,
  output ou
);

  Soma_4_btis soma_4_btis_1 (.in_1(a), .in_2(b), .out_3(soma));
  comparador comparador_1 (.in_1(a), .in_2(b), .out_3(ou));
endmodule
