// Logisim project guia6.circ as structural Verilog
module HA (
  input  a,
  input  b,
  output s0,
  output s1
);

  xor xor_1 (s0, a, b);
  and and_1 (s1, a, b);
endmodule

module CA (
  input  vai_um,
  input  a,
  input  b,
  output s0,
  output s1
);

  wire ha_1_s0, ha_1_s1, ha_2_s1;

  HA ha_1 (.a(a), .b(b), .s0(ha_1_s0), .s1(ha_1_s1));
  HA ha_2 (.a(vai_um), .b(ha_1_s0), .s0(s0), .s1(ha_2_s1));
  or or_1 (s1, ha_2_s1, ha_1_s1);

  // Notes on the sheet:
  //   2
  //   1
endmodule

module ALU (
  input  [3:0] in_1,
  input  [3:0] in_2,
  output [3:0] out_3,
  output out_4,
  output out_5
);

  wire ca_1_s1, ca_2_s1, ha_1_s1;
  wire [3:0] xnor_1_out;

  // Probe on xnor_1_out
  assign xnor_1_out = ~(in_1 ^ in_2);  // XNOR_Gate xnor_1, 4 bits wide
  HA ha_1 (.a(in_1[0]), .b(in_2[0]), .s0(out_3[0]), .s1(ha_1_s1));
  CA ca_1 (.vai_um(ha_1_s1), .a(in_1[1]), .b(in_2[1]), .s0(out_3[1]), .s1(ca_1_s1));
  CA ca_2 (.vai_um(ca_1_s1), .a(in_1[2]), .b(in_2[2]), .s0(out_3[2]), .s1(ca_2_s1));
  and and_1 (out_5, xnor_1_out[0], xnor_1_out[1], xnor_1_out[2], xnor_1_out[3]);
  CA ca_3 (.vai_um(ca_2_s1), .a(in_1[3]), .b(in_2[3]), .s0(out_3[3]), .s1(out_4));
endmodule
