// Logisim project guia6ex2.circ as structural Verilog
module SomaMeia (
  input  a,
  input  b,
  output s0,
  output s1
);

  xor xor_1 (s0, a, b);
  and and_1 (s1, a, b);
endmodule

module CA2 (
  input  vai_um,
  input  a,
  input  b,
  output s0,
  output s1
);

  wire somameia_1_s0, somameia_1_s1, somameia_2_s1;

  SomaMeia somameia_1 (.a(a), .b(b), .s0(somameia_1_s0), .s1(somameia_1_s1));
  SomaMeia somameia_2 (.a(vai_um), .b(somameia_1_s0), .s0(s0), .s1(somameia_2_s1));
  or or_1 (s1, somameia_2_s1, somameia_1_s1);

  // Notes on the sheet:
  //   2
  //   1
endmodule

module ALU (
  input  [3:0] in_1,
  input  [3:0] in_2,
  output [3:0] SOMA,
  output OVERFLOW,
  output IGUAL__1,
  output [3:0] out_6,
  output CARRY
);

  wire [3:0] xnor_1_out;

  CS4 cs4_1 (.a(in_1), .b(in_2), .out_3(out_6), .out_4(CARRY));
  CA4 ca4_1 (.a(in_1), .in_2(in_2), .soma(SOMA), .out_4(OVERFLOW));
  // Probe on xnor_1_out
  assign xnor_1_out = ~(in_1 ^ in_2);  // XNOR_Gate xnor_1, 4 bits wide
  and and_1 (IGUAL__1, xnor_1_out[0], xnor_1_out[1], xnor_1_out[2], xnor_1_out[3]);

  // Notes on the sheet:
  //   SUBTRAÇÃO
  //   DIFERENTE: 0
endmodule

module \DiferençaMeia  (
  input  in_1,
  input  in_2,
  output out_3,
  output out_4
);

  wire not_1_out;

  not not_1 (not_1_out, in_1);
  xor xor_1 (out_3, in_1, in_2);
  and and_1 (out_4, in_2, not_1_out);

  // Notes on the sheet:
  //   q
endmodule

module CS2 (
  input  c,
  input  a,
  input  b,
  output s0,
  output s1
);

  wire \diferençameia_1_out_3 , \diferençameia_1_out_4 , \diferençameia_2_out_4 ;

  \DiferençaMeia  \diferençameia_1  (
    .in_1(a), .in_2(b), .out_3(\diferençameia_1_out_3 ), .out_4(\diferençameia_1_out_4 ));
  \DiferençaMeia  \diferençameia_2  (
    .in_1(\diferençameia_1_out_3 ), .in_2(c), .out_3(s0), .out_4(\diferençameia_2_out_4 ));
  or or_1 (s1, \diferençameia_2_out_4 , \diferençameia_1_out_4 );

  // Notes on the sheet:
  //   1
  //   w1
  //   2
  //   w2
  //   w3
endmodule

module CA4 (
  input  [3:0] a,
  input  [3:0] in_2,
  output [3:0] soma,
  output out_4
);

  wire ca2_1_s1, ca2_2_s1, somameia_1_s1;

  SomaMeia somameia_1 (.a(a[0]), .b(in_2[0]), .s0(soma[0]), .s1(somameia_1_s1));
  CA2 ca2_1 (.vai_um(somameia_1_s1), .a(a[1]), .b(in_2[1]), .s0(soma[1]), .s1(ca2_1_s1));
  CA2 ca2_2 (.vai_um(ca2_1_s1), .a(a[2]), .b(in_2[2]), .s0(soma[2]), .s1(ca2_2_s1));
  CA2 ca2_3 (.vai_um(ca2_2_s1), .a(a[3]), .b(in_2[3]), .s0(out_4));  // open: s1

  assign soma[3] = out_4;
endmodule

module CS4 (
  input  [3:0] a,
  input  [3:0] b,
  output [3:0] out_3,
  output out_4
);

  wire cs2_1_s1, cs2_2_s1, \diferençameia_1_out_4 ;

  \DiferençaMeia  \diferençameia_1  (.in_1(a[0]), .in_2(b[0]), .out_3(out_3[0]), .out_4(\diferençameia_1_out_4 ));
  CS2 cs2_1 (.c(\diferençameia_1_out_4 ), .a(a[1]), .b(b[1]), .s0(out_3[1]), .s1(cs2_1_s1));
  CS2 cs2_2 (.c(cs2_1_s1), .a(a[2]), .b(b[2]), .s0(out_3[2]), .s1(cs2_2_s1));
  CS2 cs2_3 (.c(cs2_2_s1), .a(a[3]), .b(b[3]), .s0(out_3[3]), .s1(out_4));
endmodule
