// Logisim project Circuitos.circ as structural Verilog: 15 circuits, main circuit Meia-Soma(Comum)
module Meia_Soma_Comum (
  input  A,
  input  B,
  output S0,
  output S1
);

  wire and_1_out, and_2_out, not_1_out, not_2_out;

  not not_1 (not_1_out, A);
  not not_2 (not_2_out, B);
  and and_1 (and_1_out, not_1_out, B);
  and and_2 (and_2_out, A, not_2_out);
  and and_3 (S1, A, B);
  or or_1 (S0, and_1_out, and_2_out);
endmodule

module somaCompleta_Comum (
  input  A,
  input  B,
  input  C,
  output S0,
  output S1
);

  wire meia_soma_comum_1_s0, meia_soma_comum_1_s1, meia_soma_comum_2_s1;

  Meia_Soma_Comum meia_soma_comum_1 (.A(A), .B(B), .S0(meia_soma_comum_1_s0), .S1(meia_soma_comum_1_s1));
  Meia_Soma_Comum meia_soma_comum_2 (.A(meia_soma_comum_1_s0), .B(C), .S0(S0), .S1(meia_soma_comum_2_s1));
  or or_1 (S1, meia_soma_comum_2_s1, meia_soma_comum_1_s1);
endmodule

module \Meia_Difereça_Comum  (
  input  A,
  input  B,
  output S0,
  output S1
);

  wire and_1_out, and_2_out, not_1_out, not_2_out, not_3_out;

  not not_1 (not_1_out, A);
  not not_2 (not_2_out, B);
  not not_3 (not_3_out, A);
  and and_1 (and_1_out, not_1_out, B);
  and and_2 (and_2_out, A, not_2_out);
  and and_3 (S1, not_3_out, B);
  or or_1 (S0, and_1_out, and_2_out);
endmodule

module \diferençaCompleta  (
  input  A,
  input  B,
  input  C,
  output S0,
  output S1
);

  wire \meia_difereça_comum_1_s0 , \meia_difereça_comum_1_s1 , \meia_difereça_comum_2_s1 ;

  \Meia_Difereça_Comum  \meia_difereça_comum_1  (
    .A(A), .B(B), .S0(\meia_difereça_comum_1_s0 ), .S1(\meia_difereça_comum_1_s1 ));
  \Meia_Difereça_Comum  \meia_difereça_comum_2  (
    .A(\meia_difereça_comum_1_s0 ), .B(C), .S0(S0), .S1(\meia_difereça_comum_2_s1 ));
  or or_1 (S1, \meia_difereça_comum_2_s1 , \meia_difereça_comum_1_s1 );
endmodule

module meiaSoma_Nor (
  input  A,
  input  B,
  output S0,
  output S1
);

  wire nor_1_out, nor_2_out, nor_3_out, nor_4_out, nor_5_out, nor_6_out;

  nor nor_1 (nor_1_out, A, A);
  nor nor_2 (nor_2_out, B, B);
  nor nor_3 (nor_3_out, A, B);
  nor nor_4 (nor_4_out, A, A);
  nor nor_5 (nor_5_out, B, B);
  nor nor_6 (nor_6_out, nor_1_out, nor_2_out);
  nor nor_7 (S1, nor_4_out, nor_5_out);
  nor nor_8 (S0, nor_6_out, nor_3_out);
endmodule

module Somador_3bits (
  input  a3,
  input  a1,
  input  a0,
  input  b2,
  input  b1,
  input  b0,
  input  in_7,
  output S0,
  output S1,
  output S2,
  output S1_2
);

  wire somacompleta_comum_1_s1, somacompleta_comum_2_s1;

  somaCompleta_Comum somacompleta_comum_1 (.A(a0), .B(b0), .C(in_7), .S0(S0), .S1(somacompleta_comum_1_s1));
  somaCompleta_Comum somacompleta_comum_2 (
    .A(a1), .B(b1), .C(somacompleta_comum_1_s1), .S0(S1), .S1(somacompleta_comum_2_s1));
  somaCompleta_Comum somacompleta_comum_3 (.A(a3), .B(b2), .C(somacompleta_comum_2_s1), .S0(S2), .S1(S1_2));
endmodule

module Subtrator_2bits (
  input  in_1,
  input  in_2,
  input  in_3,
  input  in_4,
  input  in_5,
  output S1,
  output S1_2,
  output S1_3
);

  wire \diferençacompleta_1_s1 ;

  \diferençaCompleta  \diferençacompleta_1  (.A(in_3), .B(in_5), .C(in_1), .S0(S1), .S1(\diferençacompleta_1_s1 ));
  \diferençaCompleta  \diferençacompleta_2  (.A(in_2), .B(in_4), .C(\diferençacompleta_1_s1 ), .S0(S1_2), .S1(S1_3));
endmodule

module Multiplicador_2bits (
  input  a1,
  input  a0,
  input  b1,
  input  b0,
  input  in_5,
  output S0,
  output S1,
  output S2,
  output S3
);

  wire and_2_out, and_3_out, and_4_out, meia_soma_comum_1_s1;

  and and_1 (S0, a0, b0);
  and and_2 (and_2_out, a0, b1);
  and and_3 (and_3_out, a1, b0);
  and and_4 (and_4_out, a1, b1);
  Meia_Soma_Comum meia_soma_comum_1 (.A(and_2_out), .B(and_3_out), .S0(S1), .S1(meia_soma_comum_1_s1));
  somaCompleta_Comum somacompleta_comum_1 (.A(and_4_out), .B(in_5), .C(meia_soma_comum_1_s1), .S0(S2), .S1(S3));
endmodule

module ALU_4bits (
  input  Sinal,
  input  a2,
  input  a1,
  input  a0,
  input  Sinal_2,
  input  b2,
  input  b1,
  input  b0,
  output Diferente,
  output S0,
  output S1,
  output S2,
  output S3,
  output carry,
  output OVR,
  output zero,
  output a3_prime,
  output a2_prime,
  output a1_prime,
  output a0_prime,
  output b3_prime,
  output b2_prime,
  output b1_prime,
  output b0_prime,
  output S1_2,
  output S1_3,
  output S1_4,
  output S1_5,
  output \A____B___1___Sim_0___Não 
);

  wire somador_4bits_1_c5;

  Comparador_Logico_4_bits comparador_logico_4_bits_1 (
    .Sinal(Sinal), .a2(a2), .a1(a1), .a0(a0), .Sinal_2(Sinal_2), .b2(b2), .b1(b1), .b0(b0),
    .S0_Diferente(Diferente));
  Somador_4bits somador_4bits_1 (
    .a3(Sinal), .a2(a2), .a1(a1), .a0(a0), .b3(Sinal_2), .b2(b2), .b1(b1), .b0(b0), .S0(S0), .S1(S1),
    .S2(S2), .S3(S3), .S4(carry), .c5(somador_4bits_1_c5));
  ComplementoDeUm complementodeum_1 (
    .a3(Sinal), .a2(a2), .a1(a1), .a0(a0), .b3(Sinal_2), .b2(b2), .b1(b1), .b0(b0), .a3_prime(a3_prime),
    .a2_prime(a2_prime), .a1_prime(a1_prime), .a0_prime(a0_prime), .b3_prime(b3_prime), .b2_prime(b2_prime),
    .b1_prime(b1_prime), .b0_prime(b0_prime));
  subtrator_4bits subtrator_4bits_1 (
    .a3(Sinal), .a2(a2), .a1(a1), .a0(a0), .b3(Sinal_2), .b2(b2), .b1(b1), .b0(b0), .S0(S1_2), .S1(S1_3),
    .S2(S1_4), .S3(S1_5), .Maior___menor(\A____B___1___Sim_0___Não ));
  and and_1 (OVR, carry, somador_4bits_1_c5);
  nor nor_1 (zero, b0, b1, b2, Sinal_2, a0, a1, a2, Sinal);
endmodule

module Comparador_Logico_4_bits (
  input  Sinal,
  input  a2,
  input  a1,
  input  a0,
  input  Sinal_2,
  input  b2,
  input  b1,
  input  b0,
  output S0_Diferente
);

  wire xor_1_out, xor_2_out, xor_3_out, xor_4_out;

  xor xor_1 (xor_1_out, b0, a0);
  xor xor_2 (xor_2_out, b1, a1);
  xor xor_3 (xor_3_out, b2, a2);
  xor xor_4 (xor_4_out, Sinal_2, Sinal);
  or or_1 (S0_Diferente, xor_1_out, xor_2_out, xor_3_out, xor_4_out);

  // Notes on the sheet:
  //   É diferente? 1 - sim 0 - não
endmodule

module Somador_4bits (
  input  a3,
  input  a2,
  input  a1,
  input  a0,
  input  b3,
  input  b2,
  input  b1,
  input  b0,
  output S0,
  output S1,
  output S2,
  output S3,
  output S4,
  output c5
);

  wire somacompleta_comum_1_s1, somacompleta_comum_2_s1;

  somaCompleta_Comum somacompleta_comum_1 (.A(a0), .B(b0), .C(1'b0), .S0(S0), .S1(somacompleta_comum_1_s1));
  somaCompleta_Comum somacompleta_comum_2 (
    .A(a1), .B(b1), .C(somacompleta_comum_1_s1), .S0(S1), .S1(somacompleta_comum_2_s1));
  somaCompleta_Comum somacompleta_comum_3 (.A(a2), .B(b2), .C(somacompleta_comum_2_s1), .S0(S2), .S1(c5));
  somaCompleta_Comum somacompleta_comum_4 (.A(a3), .B(b3), .C(c5), .S0(S3), .S1(S4));
endmodule

module subtrator_4bits (
  input  a3,
  input  a2,
  input  a1,
  input  a0,
  input  b3,
  input  b2,
  input  b1,
  input  b0,
  output S0,
  output S1,
  output S2,
  output S3,
  output Maior___menor
);

  wire \diferençacompleta_1_s1 , \diferençacompleta_2_s1 , \diferençacompleta_3_s1 ;

  \diferençaCompleta  \diferençacompleta_1  (.A(a0), .B(b0), .C(1'b0), .S0(S0), .S1(\diferençacompleta_1_s1 ));
  \diferençaCompleta  \diferençacompleta_2  (
    .A(a1), .B(b1), .C(\diferençacompleta_1_s1 ), .S0(S1), .S1(\diferençacompleta_2_s1 ));
  \diferençaCompleta  \diferençacompleta_3  (
    .A(a2), .B(b2), .C(\diferençacompleta_2_s1 ), .S0(S2), .S1(\diferençacompleta_3_s1 ));
  \diferençaCompleta  \diferençacompleta_4  (.A(a3), .B(b3), .C(\diferençacompleta_3_s1 ), .S0(S3), .S1(Maior___menor));

  // Notes on the sheet:
  //   1 - a >
  //   0 a <
endmodule

module ComplementoDeUm (
  input  a3,
  input  a2,
  input  a1,
  input  a0,
  input  b3,
  input  b2,
  input  b1,
  input  b0,
  output a3_prime,
  output a2_prime,
  output a1_prime,
  output a0_prime,
  output b3_prime,
  output b2_prime,
  output b1_prime,
  output b0_prime
);

  not not_1 (a3_prime, a3);
  not not_2 (a2_prime, a2);
  not not_3 (a1_prime, a1);
  not not_4 (a0_prime, a0);
  not not_5 (b3_prime, b3);
  not not_6 (b2_prime, b2);
  not not_7 (b1_prime, b1);
  not not_8 (b0_prime, b0);
endmodule

module ALU_4_bits_compacta (
  input  a0,
  input  a1,
  input  a2,
  input  Sinal,
  input  b0,
  input  b1,
  input  b2,
  input  Sinal_2,
  output \Diferente__0___Não_1___Sim ,
  output [4:0] A___B,
  output [1:0] OVR__Zero,
  output [3:0] a_prime,
  output [3:0] b_prime,
  output [3:0] A___B_2,
  output \A___B_0___Não__1___Sim 
);

  ALU_4bits alu_4bits_1 (
    .Sinal(Sinal), .a2(a2), .a1(a1), .a0(a0), .Sinal_2(Sinal_2), .b2(b2), .b1(b1), .b0(b0),
    .Diferente(\Diferente__0___Não_1___Sim ), .S0(A___B[0]), .S1(A___B[1]), .S2(A___B[2]), .S3(A___B[3]),
    .carry(A___B[4]), .OVR(OVR__Zero[0]), .zero(OVR__Zero[1]), .a3_prime(a_prime[3]), .a2_prime(a_prime[2]),
    .a1_prime(a_prime[1]), .a0_prime(a_prime[0]), .b3_prime(b_prime[3]), .b2_prime(b_prime[2]),
    .b1_prime(b_prime[1]), .b0_prime(b_prime[0]), .S1_2(A___B_2[0]), .S1_3(A___B_2[1]), .S1_4(A___B_2[2]),
    .S1_5(A___B_2[3]), .\A____B___1___Sim_0___Não (\A___B_0___Não__1___Sim ));
endmodule

module ALU_Super_Compacta (
  input  a0,
  input  a1,
  input  a2,
  input  Sinal,
  input  b0,
  input  b1,
  input  b2,
  input  Sinal_2,
  output \Diferente_0___Não_1___Sim ,
  output [4:0] A___B,
  output [1:0] OVR__Zero,
  output [3:0] a_prime,
  output [3:0] b_prime,
  output [3:0] A___B_2,
  output \A___B_1___Sim_0_Não 
);

  ALU_4_bits_compacta alu_4_bits_compacta_1 (
    .a0(a0), .a1(a1), .a2(a2), .Sinal(Sinal), .b0(b0), .b1(b1), .b2(b2), .Sinal_2(Sinal_2),
    .\Diferente__0___Não_1___Sim (\Diferente_0___Não_1___Sim ), .A___B(A___B), .OVR__Zero(OVR__Zero),
    .a_prime(a_prime), .b_prime(b_prime), .A___B_2(A___B_2), .\A___B_0___Não__1___Sim (\A___B_1___Sim_0_Não ));
endmodule
