// Logisim project Guia06.circ as structural Verilog: 13 circuits, main circuit main
module main (
);


  // Notes on the sheet:
  //   O Ex01 Contém a Soma e os detectores de Zero, OverFlow e CarryOut
  //   O Ex02 Faz o C2 de B e Soma e depois comparando entre Maior, Menor ou Igual
  //   O SubCircuito Comparador Compara Bits por Diferente ou Iguais
  //   O SubCircuito C1 faz o Complemento de 1 do Bit (O Circuito C2 soma C1 e uma constante 4'b0001)
endmodule

module MeiaSoma (
  input  a,
  input  b,
  output s,
  output c
);

  and and_1 (c, a, b);
  xor xor_1 (s, a, b);
endmodule

module SomaCompleta (
  input  sinal,
  input  cin,
  input  a,
  input  b,
  output s,
  output c
);

  wire meiasoma_1_c, meiasoma_1_s, meiasoma_2_c, xor_1_out;

  MeiaSoma meiasoma_1 (.a(cin), .b(a), .s(meiasoma_1_s), .c(meiasoma_1_c));
  xor xor_1 (xor_1_out, sinal, b);
  MeiaSoma meiasoma_2 (.a(meiasoma_1_s), .b(xor_1_out), .s(s), .c(meiasoma_2_c));
  or or_1 (c, meiasoma_2_c, meiasoma_1_c);
endmodule

module Comparador (
  input  [3:0] a,
  input  [3:0] b,
  output igual,
  output diferente
);

  wire xnor_1_out, xnor_2_out, xnor_3_out, xnor_4_out;

  xnor xnor_1 (xnor_1_out, a[0], b[0]);
  xnor xnor_2 (xnor_2_out, a[1], b[1]);
  xnor xnor_3 (xnor_3_out, a[2], b[2]);
  xnor xnor_4 (xnor_4_out, a[3], b[3]);
  and and_1 (igual, xnor_1_out, xnor_2_out, xnor_3_out, xnor_4_out);
  not not_1 (diferente, igual);
endmodule

module Ex01 (
  input  [3:0] a,
  input  [3:0] b,
  output [3:0] S,
  output Zero,
  output cout,
  output overflow
);

  wire not_1_out, somacompleta_1_c, somacompleta_2_c, somacompleta_3_c, somacompleta_4_c;

  SomaCompleta somacompleta_1 (.cin(1'b0), .a(a[0]), .b(b[0]), .s(S[0]), .c(somacompleta_1_c));  // open: sinal
  SomaCompleta somacompleta_2 (
    .cin(somacompleta_1_c), .a(a[1]), .b(b[1]), .sinal(1'b0), .s(S[1]), .c(somacompleta_2_c));
  SomaCompleta somacompleta_3 (
    .cin(somacompleta_2_c), .a(a[2]), .b(b[2]), .sinal(1'b0), .s(S[2]), .c(somacompleta_3_c));
  SomaCompleta somacompleta_4 (
    .cin(somacompleta_3_c), .a(a[3]), .b(b[3]), .sinal(1'b0), .s(S[3]), .c(somacompleta_4_c));
  not not_1 (not_1_out, somacompleta_4_c);
  xor xor_1 (overflow, somacompleta_4_c, somacompleta_3_c);
  Zero zero_1 (.a(S), .Zero(Zero));
  and and_1 (cout, somacompleta_4_c, not_1_out);
endmodule

module MeiaDif (
  input  a,
  input  b,
  output s,
  output c
);

  wire not_1_out;

  not not_1 (not_1_out, a);
  xor xor_1 (s, a, b);
  and and_1 (c, not_1_out, b);
endmodule

module DifCompleta (
  input  Sinal,
  input  a,
  input  b,
  input  cin,
  output s,
  output c
);

  wire meiadif_1_c, meiadif_1_s, meiadif_2_c, xor_1_out;

  xor xor_1 (xor_1_out, Sinal, b);
  MeiaDif meiadif_1 (.a(a), .b(xor_1_out), .s(meiadif_1_s), .c(meiadif_1_c));
  MeiaDif meiadif_2 (.a(meiadif_1_s), .b(cin), .s(s), .c(meiadif_2_c));
  or or_1 (c, meiadif_2_c, meiadif_1_c);
endmodule

module Zero (
  input  [3:0] a,
  output Zero
);

  wire nor_1_out, nor_2_out, nor_3_out, nor_4_out;

  not nor_1 (nor_1_out, a[0]);  // NOR_Gate
  not nor_2 (nor_2_out, a[1]);  // NOR_Gate
  not nor_3 (nor_3_out, a[2]);  // NOR_Gate
  not nor_4 (nor_4_out, a[3]);  // NOR_Gate
  and and_1 (Zero, nor_1_out, nor_2_out, nor_3_out, nor_4_out);
endmodule

module C2 (
  input  [3:0] a,
  output [3:0] s
);

  wire [3:0] not_1_out;

  assign not_1_out = ~a;  // NOT_Gate not_1, 4 bits wide
  Ex01 ex01_1 (.a(not_1_out), .b(4'b0001), .S(s));  // open: Zero, cout, overflow
endmodule

module C1 (
  input  [3:0] a,
  output [3:0] s
);

  assign s = ~a;  // NOT_Gate not_1, 4 bits wide
endmodule

module AND (
  input  [3:0] in_1,
  input  [3:0] in_2,
  output [3:0] out_3
);

  assign out_3 = in_1 & in_2;  // AND_Gate and_1, 4 bits wide
endmodule

module OR (
  input  [3:0] a,
  input  [3:0] b,
  output [3:0] out_3
);

  assign out_3 = a | b;  // OR_Gate or_1, 4 bits wide
endmodule

module Ex02 (
  input  [3:0] a,
  input  [3:0] b,
  output Iguais,
  output Menor,
  output Maior
);

  wire not_1_out, not_2_out, somacompleta_1_c, somacompleta_2_c, somacompleta_3_c;
  wire [2:0] somacompleta_1_s;
  wire [3:0] c2_1_s;

  C2 c2_1 (.a(b), .s(c2_1_s));
  SomaCompleta somacompleta_1 (
    .cin(1'b0), .a(a[0]), .b(c2_1_s[0]), .s(somacompleta_1_s[0]), .c(somacompleta_1_c));  // open: sinal
  SomaCompleta somacompleta_2 (
    .cin(somacompleta_1_c), .a(a[1]), .b(c2_1_s[1]), .s(somacompleta_1_s[1]), .c(somacompleta_2_c));  // open: sinal
  SomaCompleta somacompleta_3 (
    .cin(somacompleta_2_c), .a(a[2]), .b(c2_1_s[2]), .s(somacompleta_1_s[2]), .c(somacompleta_3_c));  // open: sinal
  SomaCompleta somacompleta_4 (.cin(somacompleta_3_c), .a(a[3]), .b(c2_1_s[3]), .s(Menor));  // open: sinal, c
  // Probe on {Menor, somacompleta_1_s}
  Zero zero_1 (.a({Menor, somacompleta_1_s}), .Zero(Iguais));
  not not_1 (not_1_out, Iguais);
  not not_2 (not_2_out, Menor);
  and and_1 (Maior, not_2_out, not_1_out);

  // Notes on the sheet:
  //   a < b
  //   a > b
endmodule
