// Logisim project Exercicio01_guia6.circ as structural Verilog
module meia_soma (
  input  a,
  input  b,
  output s1,
  output s0
);

  xor xor_1 (s1, a, b);
  and and_1 (s0, a, a, b);
endmodule

module soma_completa (
  input  carry_in,
  input  a,
  input  b,
  output s1,
  output s0
);

  wire meia_soma_1_s0, meia_soma_1_s1, meia_soma_2_s0;

  meia_soma meia_soma_1 (.a(a), .b(b), .s1(meia_soma_1_s1), .s0(meia_soma_1_s0));
  meia_soma meia_soma_2 (.a(carry_in), .b(meia_soma_1_s1), .s1(s1), .s0(meia_soma_2_s0));
  or or_1 (s0, meia_soma_2_s0, meia_soma_1_s0);
endmodule

module soma4bits (
  input  [3:0] a,
  input  [3:0] b,
  output [3:0] resultado
);

  wire meia_soma_1_s0, soma_completa_1_s0, soma_completa_2_s0;

  meia_soma meia_soma_1 (.a(a[0]), .b(b[0]), .s1(resultado[0]), .s0(meia_soma_1_s0));
  soma_completa soma_completa_1 (
    .carry_in(meia_soma_1_s0), .a(a[1]), .b(b[1]), .s1(resultado[1]), .s0(soma_completa_1_s0));
  soma_completa soma_completa_2 (
    .carry_in(soma_completa_1_s0), .a(a[2]), .b(b[2]), .s1(resultado[2]), .s0(soma_completa_2_s0));
  soma_completa soma_completa_3 (.carry_in(soma_completa_2_s0), .a(a[3]), .b(b[3]), .s1(resultado[3]));  // open: s0
endmodule

module comparar (
  input  [3:0] a,
  input  [3:0] b,
  output _0_diferentes,
  output [3:0] resultado
);

  wire [3:0] xnor_1_out;

  assign xnor_1_out = ~(a ^ b);  // XNOR_Gate xnor_1, 4 bits wide
  soma4bits soma4bits_1 (.a(a), .b(b), .resultado(resultado));
  and and_1 (_0_diferentes, xnor_1_out[0], xnor_1_out[1], xnor_1_out[2], xnor_1_out[3]);

  // Notes on the sheet:
  //   1-iguais
endmodule

module \meia_diferença  (
  input  a,
  input  b,
  output s0,
  output s1
);

  wire not_1_out;

  not not_1 (not_1_out, a);
  xor xor_1 (s0, a, b);
  and and_1 (s1, b, not_1_out);
endmodule

module \diferença_completa  (
  input  carry,
  input  a,
  input  b,
  output s0,
  output s1
);

  wire and_1_out, and_2_out, not_1_out, not_2_out, xor_1_out;

  xor xor_1 (xor_1_out, a, b);
  not not_1 (not_1_out, a);
  and and_1 (and_1_out, not_1_out, b);
  not not_2 (not_2_out, xor_1_out);
  xor xor_2 (s0, carry, xor_1_out);
  and and_2 (and_2_out, carry, not_2_out);
  or or_1 (s1, and_2_out, and_1_out);
endmodule

module \diferença4bits  (
  input  [3:0] a,
  input  [3:0] b,
  output [3:0] Resultado,
  output out_4
);

  wire \diferença_completa_1_s1 , \diferença_completa_2_s1 , \meia_diferença_1_s1 ;

  \meia_diferença  \meia_diferença_1  (.a(a[0]), .b(b[0]), .s0(Resultado[0]), .s1(\meia_diferença_1_s1 ));
  \diferença_completa  \diferença_completa_1  (
    .carry(\meia_diferença_1_s1 ), .a(a[1]), .b(b[1]), .s0(Resultado[1]), .s1(\diferença_completa_1_s1 ));
  \diferença_completa  \diferença_completa_2  (
    .carry(\diferença_completa_1_s1 ), .a(a[2]), .b(b[2]), .s0(Resultado[2]), .s1(\diferença_completa_2_s1 ));
  \diferença_completa  \diferença_completa_3  (
    .carry(\diferença_completa_2_s1 ), .a(a[3]), .b(b[3]), .s0(out_4));  // open: s1

  assign Resultado[3] = out_4;
endmodule

module \comparar_diferença  (
  input  in_1,
  input  in_2,
  output out_3
);

  wire nand_1_out;

  // NOT_Gate not_1 is placed but not wired
  // NOT_Gate not_2 is placed but not wired
  // AND_Gate and_1 is placed but not wired
  nand nand_1 (nand_1_out, in_1, in_2);
  or or_1 (out_3, nand_1_out, in_2);
  // NOR_Gate nor_1 is placed but not wired
endmodule
