// Logisim project Guia06_01.circ as structural Verilog: 4 circuits, main circuit Full_Adder
module Full_Adder (
  input  Cin,
  input  A,
  input  B,
  output s0,
  output Cout
);

  wire half_adder2_1_s3, half_adder_1_s4, half_adder_1_s5;

  Half_Adder half_adder_1 (.x(A), .y(B), .s4(half_adder_1_s4), .s5(half_adder_1_s5));
  Half_Adder2 half_adder2_1 (.Vai_um(Cin), .x(half_adder_1_s4), .s2(s0), .s3(half_adder2_1_s3));
  or or_1 (Cout, half_adder2_1_s3, half_adder_1_s5);
endmodule

module Half_Adder (
  input  x,
  input  y,
  output s4,
  output s5
);

  xor xor_1 (s4, x, y);
  and and_1 (s5, y, x);
endmodule

module Half_Adder2 (
  input  Vai_um,
  input  x,
  output s2,
  output s3
);

  xor xor_1 (s2, Vai_um, x);
  and and_1 (s3, x, Vai_um);
endmodule

module ALU_4bits (
  input  Cin,
  input  A,
  input  B,
  input  A_2,
  input  B_2,
  input  A_3,
  input  B_3,
  input  A_4,
  input  B_4,
  output Comp,
  output s0,
  output s1,
  output Comp2,
  output s2,
  output Comp3,
  output s3,
  output Cout,
  output Comp4
);

  wire full_adder_1_cout, full_adder_2_cout, full_adder_3_cout;

  nor nor_1 (Comp, A, B);
  Full_Adder full_adder_1 (.Cin(Cin), .A(A), .B(B), .s0(s0), .Cout(full_adder_1_cout));
  Full_Adder full_adder_2 (.Cin(full_adder_1_cout), .A(A_2), .B(B_2), .s0(s1), .Cout(full_adder_2_cout));
  Full_Adder full_adder_3 (.Cin(full_adder_2_cout), .A(A_3), .B(B_3), .s0(s2), .Cout(full_adder_3_cout));
  Full_Adder full_adder_4 (.Cin(full_adder_3_cout), .A(A_4), .B(B_4), .s0(s3), .Cout(Cout));
  nor nor_2 (Comp3, A_3, B_3);
  nor nor_3 (Comp4, A_4, B_4);
  nor nor_4 (Comp2, A_2, B_2);
endmodule
