// Logisim project Guia06_02_03.circ as structural Verilog: 5 circuits, main circuit Full_Adder
module Full_Adder (
  input  Cin,
  input  A,
  input  B,
  output s0,
  output Cout
);

  wire half_adder2_1_s3, half_adder_1_s4, half_adder_1_s5;

  Half_Adder half_adder_1 (.x(A), .y(B), .s4(half_adder_1_s4), .s5(half_adder_1_s5));
  Half_Adder2 half_adder2_1 (.Vai_um(Cin), .x(half_adder_1_s4), .s2(s0), .s3(half_adder2_1_s3));
  or or_1 (Cout, half_adder2_1_s3, half_adder_1_s5);
endmodule

module Half_Adder (
  input  x,
  input  y,
  output s4,
  output s5
);

  xor xor_1 (s4, x, y);
  and and_1 (s5, y, x);
endmodule

module Half_Adder2 (
  input  Vai_um,
  input  x,
  output s2,
  output s3
);

  xor xor_1 (s2, Vai_um, x);
  and and_1 (s3, x, Vai_um);
endmodule

module ALU_4bits (
  input  Cin,
  input  A0,
  input  B0,
  input  A1,
  input  B1,
  input  A0_2,
  input  B0_2,
  input  A1_2,
  input  B1_2,
  output s0,
  output Comp0,
  output Comp1,
  output s1,
  output s2,
  output Comp0_2,
  output Comp1_2,
  output s3,
  output zero,
  output Cout,
  output Overflow
);

  wire full_adder_1_cout, full_adder_2_cout, full_adder_3_cout, not_1_out, not_2_out, not_3_out, not_4_out;

  not not_1 (not_1_out, B0);
  not not_2 (not_2_out, B1);
  not not_3 (not_3_out, B0_2);
  not not_4 (not_4_out, B1_2);
  Full_Adder full_adder_1 (.Cin(Cin), .A(A0), .B(not_1_out), .s0(s0), .Cout(full_adder_1_cout));
  Full_Adder full_adder_2 (.Cin(full_adder_1_cout), .A(A1), .B(not_2_out), .s0(s1), .Cout(full_adder_2_cout));
  Full_Adder full_adder_3 (.Cin(full_adder_2_cout), .A(A0_2), .B(not_3_out), .s0(s2), .Cout(full_adder_3_cout));
  Full_Adder full_adder_4 (.Cin(full_adder_3_cout), .A(A1_2), .B(not_4_out), .s0(s3), .Cout(Cout));
  Comparator comparator_1 (.b1(B1), .b0(B0), .a1(A1), .a0(A0), .s(Comp0), .s1(Comp1));
  Comparator comparator_2 (.b1(B1_2), .b0(B0_2), .a1(A1_2), .a0(A0_2), .s(Comp0_2), .s1(Comp1_2));
  xor xor_1 (Overflow, Cin, Cout);
  xor xor_2 (zero, s3, Overflow);

  // Notes on the sheet:
  //   Cin 1- Subtrator / 0 - Adder
endmodule

module Comparator (
  input  a1,
  input  a0,
  input  b1,
  input  b0,
  output s,
  output s1
);

  wire and_1_out, and_2_out, and_3_out, and_4_out, and_5_out, and_6_out, not_1_out, not_2_out, not_3_out,
       not_4_out;

  not not_1 (not_1_out, b1);
  not not_2 (not_2_out, b0);
  not not_3 (not_3_out, a1);
  not not_4 (not_4_out, a0);
  and and_1 (and_1_out, b1, not_3_out);
  and and_2 (and_2_out, b0, not_4_out, not_3_out);
  and and_3 (and_3_out, not_4_out, b0, b1);
  and and_4 (and_4_out, a1, a0, not_2_out);
  and and_5 (and_5_out, not_1_out, a1);
  and and_6 (and_6_out, a0, not_1_out, not_2_out);
  or or_1 (s1, and_1_out, and_2_out, and_3_out);
  or or_2 (s, and_4_out, and_5_out, and_6_out);
endmodule
