// Logisim project exercicioguia07_um.circ as structural Verilog: 1 circuit, main circuit exerciciogui_07_um.circ
module exerciciogui_07_um_circ (
  input  in_1,
  input  in_2,
  input  in_3,
  input  in_4,
  input  in_5,
  output out_6
);

  wire and_1_out, and_2_out, or_2_out, undriven, undriven_2, undriven_3, undriven_4, xor_1_out, xor_2_out;

  ExactlyOne xor_1 (.out(xor_1_out), .in1(undriven_4), .in2(undriven_3), .in3(undriven_2), .in4(undriven));
  ExactlyOne xor_2 (.out(xor_2_out), .in0(undriven_4), .in1(undriven_3), .in2(undriven_2), .in3(undriven));
  and and_1 (and_1_out, undriven_4, undriven_3, undriven_2, undriven);
  and and_2 (and_2_out, undriven_4, in_5, undriven_2, undriven);
  or or_1 (out_6, xor_1_out, xor_2_out);
  buf or_2 (or_2_out, and_1_out);  // OR_Gate

  // Notes on the sheet:
  //   OBS.: POSICIONAR AS CONEXOES DE ACORDO (DEVEM FICAR VERDES)
endmodule
