// Logisim project ULA2 Logisim.circ as structural Verilog: 21 circuits, main circuit main
module main (
);


  // Notes on the sheet:
  //   Andre Sulivam - 391998
endmodule

module Soma (
  input  C,
  input  A,
  input  B,
  output S0,
  output S1
);

  wire and_1_out, and_2_out, xor_1_out;

  and and_1 (and_1_out, A, B);
  xor xor_1 (xor_1_out, A, B);
  and and_2 (and_2_out, xor_1_out, C);
  xor xor_2 (S0, C, xor_1_out);
  or or_1 (S1, and_2_out, and_1_out);

  // Notes on the sheet:
  //   Andre Sulivam - 391998
endmodule

module Soma_Sub4bits (
  input  \Soma_Subtração ,
  input  [3:0] A,
  input  [3:0] B,
  output [3:0] S,
  output Carry_Out
);

  wire soma_1_s1, soma_2_s1, soma_3_s1, xor_1_out, xor_2_out, xor_3_out, xor_4_out;

  xor xor_1 (xor_1_out, \Soma_Subtração , B[0]);
  xor xor_2 (xor_2_out, \Soma_Subtração , B[1]);
  xor xor_3 (xor_3_out, \Soma_Subtração , B[2]);
  xor xor_4 (xor_4_out, \Soma_Subtração , B[3]);
  Soma soma_1 (.C(\Soma_Subtração ), .A(A[0]), .B(xor_1_out), .S0(S[0]), .S1(soma_1_s1));
  Soma soma_2 (.C(soma_1_s1), .A(A[1]), .B(xor_2_out), .S0(S[1]), .S1(soma_2_s1));
  Soma soma_3 (.C(soma_2_s1), .A(A[2]), .B(xor_3_out), .S0(S[2]), .S1(soma_3_s1));
  Soma soma_4 (.C(soma_3_s1), .A(A[3]), .B(xor_4_out), .S0(S[3]), .S1(Carry_Out));

  // Notes on the sheet:
  //   Andre Sulivam - 391998
endmodule

module Comparador (
  input  Igual_Diferente,
  input  [3:0] A,
  input  [3:0] B,
  output out_4
);

  wire or_1_out, xor_1_out, xor_2_out, xor_3_out, xor_4_out;

  xor xor_1 (xor_1_out, A[0], B[0]);
  xor xor_2 (xor_2_out, A[1], B[1]);
  xor xor_3 (xor_3_out, A[2], B[2]);
  xor xor_4 (xor_4_out, A[3], B[3]);
  or or_1 (or_1_out, xor_1_out, xor_2_out, xor_3_out, xor_4_out);
  xnor xnor_1 (out_4, Igual_Diferente, or_1_out);

  // Notes on the sheet:
  //   Andre Sulivam - 391998
endmodule

module Carry (
  input  \Soma_Subtração ,
  input  [3:0] A,
  input  [3:0] B,
  output [3:0] S,
  output Cout,
  output Carry
);

  wire not_1_out, or_1_out, soma_1_s1, soma_2_s1, soma_3_s1, xor_1_out, xor_2_out, xor_3_out, xor_4_out;

  xor xor_1 (xor_1_out, \Soma_Subtração , B[0]);
  xor xor_2 (xor_2_out, \Soma_Subtração , B[1]);
  xor xor_3 (xor_3_out, \Soma_Subtração , B[2]);
  xor xor_4 (xor_4_out, \Soma_Subtração , B[3]);
  Soma soma_1 (.C(\Soma_Subtração ), .A(A[0]), .B(xor_1_out), .S0(S[0]), .S1(soma_1_s1));
  Soma soma_2 (.C(soma_1_s1), .A(A[1]), .B(xor_2_out), .S0(S[1]), .S1(soma_2_s1));
  Soma soma_3 (.C(soma_2_s1), .A(A[2]), .B(xor_3_out), .S0(S[2]), .S1(soma_3_s1));
  Soma soma_4 (.C(soma_3_s1), .A(A[3]), .B(xor_4_out), .S0(S[3]), .S1(Cout));
  not not_1 (not_1_out, \Soma_Subtração );
  or or_1 (or_1_out, soma_1_s1, soma_2_s1, soma_3_s1);
  and and_1 (Carry, or_1_out, not_1_out);

  // Notes on the sheet:
  //   Andre Sulivam - 391998
endmodule

module Zero (
  input  \Soma_Subtração ,
  input  [3:0] A,
  input  [3:0] B,
  output Zero,
  output [3:0] S,
  output Overflow,
  output Carry
);

  wire not_1_out, or_1_out, soma_1_s1, soma_2_s1, soma_3_s1, soma_4_s1, xor_1_out, xor_2_out, xor_3_out,
       xor_4_out;

  xor xor_1 (xor_1_out, \Soma_Subtração , B[0]);
  xor xor_2 (xor_2_out, \Soma_Subtração , B[1]);
  xor xor_3 (xor_3_out, \Soma_Subtração , B[2]);
  xor xor_4 (xor_4_out, \Soma_Subtração , B[3]);
  nor nor_1 (Zero, S[0], S[1], S[2], S[3]);
  Soma soma_1 (.C(\Soma_Subtração ), .A(A[0]), .B(xor_1_out), .S0(S[0]), .S1(soma_1_s1));
  Soma soma_2 (.C(soma_1_s1), .A(A[1]), .B(xor_2_out), .S0(S[1]), .S1(soma_2_s1));
  Soma soma_3 (.C(soma_2_s1), .A(A[2]), .B(xor_3_out), .S0(S[2]), .S1(soma_3_s1));
  Soma soma_4 (.C(soma_3_s1), .A(A[3]), .B(xor_4_out), .S0(S[3]), .S1(soma_4_s1));
  or or_1 (or_1_out, soma_1_s1, soma_2_s1, soma_3_s1);
  not not_1 (not_1_out, \Soma_Subtração );
  and and_1 (Carry, or_1_out, not_1_out);
  xor xor_5 (Overflow, soma_3_s1, soma_4_s1);

  // Notes on the sheet:
  //   Andre Sulivam - 391998
endmodule

module Overflow (
  input  \Soma_Subtração ,
  input  [3:0] A,
  input  [3:0] B,
  output Zero,
  output [3:0] S,
  output Overflow,
  output Carry
);

  wire not_1_out, or_1_out, soma_1_s1, soma_2_s1, soma_3_s1, soma_4_s1, xor_1_out, xor_2_out, xor_3_out,
       xor_4_out;

  xor xor_1 (xor_1_out, \Soma_Subtração , B[0]);
  xor xor_2 (xor_2_out, \Soma_Subtração , B[1]);
  xor xor_3 (xor_3_out, \Soma_Subtração , B[2]);
  xor xor_4 (xor_4_out, \Soma_Subtração , B[3]);
  nor nor_1 (Zero, S[0], S[1], S[2], S[3]);
  Soma soma_1 (.C(\Soma_Subtração ), .A(A[0]), .B(xor_1_out), .S0(S[0]), .S1(soma_1_s1));
  Soma soma_2 (.C(soma_1_s1), .A(A[1]), .B(xor_2_out), .S0(S[1]), .S1(soma_2_s1));
  Soma soma_3 (.C(soma_2_s1), .A(A[2]), .B(xor_3_out), .S0(S[2]), .S1(soma_3_s1));
  Soma soma_4 (.C(soma_3_s1), .A(A[3]), .B(xor_4_out), .S0(S[3]), .S1(soma_4_s1));
  or or_1 (or_1_out, soma_1_s1, soma_2_s1, soma_3_s1);
  not not_1 (not_1_out, \Soma_Subtração );
  and and_1 (Carry, or_1_out, not_1_out);
  xor xor_5 (Overflow, soma_3_s1, soma_4_s1);

  // Notes on the sheet:
  //   Andre Sulivam - 391998
endmodule

module Complemento (
  input  A_prime_B_prime,
  input  [3:0] A,
  input  [3:0] B,
  output [3:0] out_4
);

  wire and_1_out, and_2_out, and_3_out, and_4_out, and_5_out, and_6_out, and_7_out, and_8_out, not_1_out,
       not_2_out, not_3_out, not_4_out, not_5_out, not_6_out, not_7_out, not_8_out, not_9_out;

  and and_1 (and_1_out, not_3_out, not_1_out);
  not not_1 (not_1_out, A[3]);
  not not_2 (not_2_out, A[2]);
  not not_3 (not_3_out, A_prime_B_prime);
  and and_2 (and_2_out, not_3_out, not_5_out);
  and and_3 (and_3_out, not_3_out, not_2_out);
  not not_4 (not_4_out, A[0]);
  not not_5 (not_5_out, A[1]);
  and and_4 (and_4_out, not_3_out, not_4_out);
  or or_1 (out_4[3], and_1_out, and_6_out);
  not not_6 (not_6_out, B[3]);
  not not_7 (not_7_out, B[0]);
  not not_8 (not_8_out, B[2]);
  not not_9 (not_9_out, B[1]);
  and and_5 (and_5_out, A_prime_B_prime, not_8_out);
  and and_6 (and_6_out, A_prime_B_prime, not_6_out);
  or or_2 (out_4[1], and_2_out, and_7_out);
  or or_3 (out_4[2], and_3_out, and_5_out);
  and and_7 (and_7_out, A_prime_B_prime, not_9_out);
  and and_8 (and_8_out, A_prime_B_prime, not_7_out);
  or or_4 (out_4[0], and_4_out, and_8_out);

  // Notes on the sheet:
  //   Andre Sulivam - 391998
endmodule

module AND (
  input  [3:0] A,
  input  [3:0] B,
  output [3:0] AND
);

  and and_1 (AND[0], A[0], B[0]);
  and and_2 (AND[1], A[1], B[1]);
  and and_3 (AND[2], A[2], B[2]);
  and and_4 (AND[3], A[3], B[3]);

  // Notes on the sheet:
  //   Andre Sulivam - 391998
endmodule

module OR (
  input  [3:0] A,
  input  [3:0] B,
  output [3:0] OR
);

  or or_1 (OR[0], A[0], B[0]);
  or or_2 (OR[1], A[1], B[1]);
  or or_3 (OR[2], A[2], B[2]);
  or or_4 (OR[3], A[3], B[3]);

  // Notes on the sheet:
  //   Andre Sulivam - 391998
endmodule

module mux_part1 (
  input  [2:0] MUX,
  input  [3:0] S,
  input  Carry,
  input  Zero,
  input  Overflow,
  output S0,
  output S1,
  output S2,
  output S3,
  output Carry1,
  output Zero1,
  output Overflow_2
);

  wire not_1_out, not_2_out, not_3_out, or_1_out;

  not not_1 (not_1_out, MUX[2]);
  not not_2 (not_2_out, MUX[1]);
  not not_3 (not_3_out, MUX[0]);
  or or_1 (or_1_out, not_3_out, MUX[0]);
  and and_1 (S0, or_1_out, not_2_out, not_1_out, S[0], S[0]);
  and and_2 (S1, or_1_out, not_2_out, not_1_out, S[1]);
  and and_3 (S2, or_1_out, not_2_out, not_1_out, S[2]);
  and and_4 (S3, or_1_out, not_2_out, not_1_out, S[3]);
  and and_5 (Carry1, or_1_out, not_2_out, not_1_out, Carry);
  and and_6 (Zero1, or_1_out, not_2_out, not_1_out, Zero);
  and and_7 (Overflow_2, or_1_out, not_2_out, not_1_out, Overflow);

  // Notes on the sheet:
  //   Andre Sulivam - 391998
endmodule

module mux_part2 (
  input  [2:0] MUX,
  input  [3:0] Complemento,
  output S0,
  output S1,
  output S3,
  output S4
);

  wire not_1_out, not_2_out, or_1_out;

  not not_1 (not_1_out, MUX[2]);
  not not_2 (not_2_out, MUX[0]);
  or or_1 (or_1_out, not_2_out, MUX[0]);
  and and_1 (S0, or_1_out, MUX[1], not_1_out, Complemento[0]);
  and and_2 (S1, or_1_out, MUX[1], not_1_out, Complemento[1]);
  and and_3 (S3, or_1_out, MUX[1], not_1_out, Complemento[2]);
  and and_4 (S4, or_1_out, not_1_out, MUX[1], Complemento[3]);

  // Notes on the sheet:
  //   Andre Sulivam - 391998
endmodule

module mux_part3 (
  input  [2:0] MUX,
  input  Comparador,
  output S0
);

  wire not_1_out, not_2_out, or_1_out;

  not not_1 (not_1_out, MUX[1]);
  not not_2 (not_2_out, MUX[0]);
  or or_1 (or_1_out, not_2_out, MUX[0]);
  and and_1 (S0, or_1_out, not_1_out, MUX[2], Comparador);

  // Notes on the sheet:
  //   Andre Sulivam - 391998
endmodule

module mux_part4 (
  input  [2:0] MUX,
  input  [3:0] AND,
  output S0,
  output S1,
  output S3,
  output S4
);

  wire not_1_out;

  not not_1 (not_1_out, MUX[0]);
  and and_1 (S0, not_1_out, MUX[1], MUX[2], AND[0]);
  and and_2 (S1, not_1_out, MUX[1], MUX[2], AND[1]);
  and and_3 (S3, not_1_out, MUX[1], MUX[2], AND[2]);
  and and_4 (S4, not_1_out, MUX[2], MUX[1], AND[3]);
endmodule

module mux_final (
  input  [2:0] MUX,
  input  [3:0] S,
  input  Carry,
  input  Zero,
  input  Overflow,
  input  [3:0] Complemento,
  input  [3:0] AND,
  input  [3:0] OR,
  input  Comparador,
  output [6:0] Saida
);

  wire mux_part1_1_s0, mux_part1_1_s1, mux_part1_1_s2, mux_part1_1_s3, mux_part2_1_s0, mux_part2_1_s1,
       mux_part2_1_s3, mux_part2_1_s4, mux_part3_1_s0, mux_part4_1_s0, mux_part4_1_s1, mux_part4_1_s3,
       mux_part4_1_s4, mux_part5_1_s0, mux_part5_1_s1, mux_part5_1_s3, mux_part5_1_s4;

  mux_part1 mux_part1_1 (
    .S(S), .Carry(Carry), .Zero(Zero), .Overflow(Overflow), .MUX(MUX), .S0(mux_part1_1_s0),
    .S1(mux_part1_1_s1), .S2(mux_part1_1_s2), .S3(mux_part1_1_s3), .Carry1(Saida[4]), .Zero1(Saida[5]),
    .Overflow_2(Saida[6]));
  mux_part2 mux_part2_1 (
    .Complemento(Complemento), .MUX(MUX), .S0(mux_part2_1_s0), .S1(mux_part2_1_s1), .S3(mux_part2_1_s3),
    .S4(mux_part2_1_s4));
  mux_part4 mux_part4_1 (
    .AND(AND), .MUX(MUX), .S0(mux_part4_1_s0), .S1(mux_part4_1_s1), .S3(mux_part4_1_s3), .S4(mux_part4_1_s4));
  mux_part5 mux_part5_1 (
    .OR(OR), .MUX(MUX), .S0(mux_part5_1_s0), .S1(mux_part5_1_s1), .S3(mux_part5_1_s3), .S4(mux_part5_1_s4));
  mux_part3 mux_part3_1 (.Comparador(Comparador), .MUX(MUX), .S0(mux_part3_1_s0));
  or or_1 (Saida[0], mux_part1_1_s0, mux_part2_1_s0, mux_part4_1_s0, mux_part5_1_s0, mux_part3_1_s0);
  or or_2 (Saida[1], mux_part1_1_s1, mux_part2_1_s1, mux_part4_1_s1, mux_part5_1_s1);
  or or_3 (Saida[2], mux_part1_1_s2, mux_part2_1_s3, mux_part4_1_s3, mux_part5_1_s3);
  or or_4 (Saida[3], mux_part1_1_s3, mux_part2_1_s4, mux_part4_1_s4, mux_part5_1_s4);

  // Notes on the sheet:
  //   Andre Sulivam - 391998
endmodule

module mux_part5 (
  input  [2:0] MUX,
  input  [3:0] OR,
  output S0,
  output S1,
  output S3,
  output S4
);

  and and_1 (S0, MUX[0], MUX[1], MUX[2], OR[0]);
  and and_2 (S1, MUX[0], MUX[1], MUX[2], OR[1]);
  and and_3 (S3, MUX[0], MUX[1], MUX[2], OR[2]);
  and and_4 (S4, MUX[0], MUX[2], MUX[1], OR[3]);

  // Notes on the sheet:
  //   Andre Sulivam - 391998
endmodule

module ULA_4bits (
  input  [3:0] MUX,
  input  [3:0] A,
  input  [3:0] B,
  output [6:0] O_Z_C_S3S2S1S0
);

  wire comparador_1_out_4, overflow_1_carry, overflow_1_overflow, overflow_1_zero;
  wire [3:0] and_1_and, complemento_1_out_4, or_1_or, overflow_1_s;
  wire [6:0] mux_final_1_saida, undriven;

  Complemento_de_2 complemento_de_2_1 ();  // open: B, A, A_B, S
  Incremento incremento_1 ();  // open: A_B, A, B, plus_1
  Decremento decremento_1 ();  // open: A_B, A, B, minus_1
  Overflow overflow_1 (
    .Zero(overflow_1_zero), .\Soma_Subtração (MUX[0]), .A(A), .B(B), .Overflow(overflow_1_overflow),
    .S(overflow_1_s), .Carry(overflow_1_carry));
  Comparador comparador_1 (.Igual_Diferente(MUX[0]), .A(A), .B(B), .out_4(comparador_1_out_4));
  Complemento complemento_1 (.A_prime_B_prime(MUX[0]), .A(A), .B(B), .out_4(complemento_1_out_4));
  AND and_1 (.A(B), .B(A), .AND(and_1_and));
  OR or_1 (.A(B), .B(A), .OR(or_1_or));
  Produto produto_1 ();  // open: A, _2A_2B, B, Produto
  mux_final mux_final_1 (
    .MUX(MUX[2:0]), .S(overflow_1_s), .Carry(overflow_1_carry), .Zero(overflow_1_zero),
    .Overflow(overflow_1_overflow), .Complemento(complemento_1_out_4), .AND(and_1_and), .OR(or_1_or),
    .Comparador(comparador_1_out_4), .Saida(mux_final_1_saida));
  Multiplexer #(.select(1), .width(7)) multiplexer_1 (
    .in0(mux_final_1_saida), .in1(undriven), .out(O_Z_C_S3S2S1S0), .sel(MUX[3]));

  // Notes on the sheet:
  //   Tabela de comandos
  //   000 - Soma
  //   001- Subtração
  //   010- Complemento A
  //   011- Complemento B
  //   100- Compara =
  //   101- Compara !=
  //   110 - And
  //   111- Or
  //   Andre Sulivam - 391998
  //   O - Overflow
  //   Z -Zero
  //   C - Carry
  //   S3 - Saida s3
  //   S2 - Saida s2
  //   S1 - Saida s1
  //   S0 - Saida s0
endmodule

module Complemento_de_2 (
  input  [3:0] B,
  input  [3:0] A,
  input  A_B,
  output [3:0] S
);

  wire [3:0] complemento_1_out_4;

  Complemento complemento_1 (.A_prime_B_prime(A_B), .A(A), .B(B), .out_4(complemento_1_out_4));
  Soma_Sub4bits soma_sub4bits_1 (
    .\Soma_Subtração (1'b0), .A(4'b0001), .B(complemento_1_out_4), .S(S));  // open: Carry_Out

  // Notes on the sheet:
  //   Andre Sulivam - 391998
endmodule

module Incremento (
  input  A_B,
  input  [3:0] A,
  input  [3:0] B,
  output [3:0] plus_1
);

  wire not_1_out;
  wire [3:0] and_4_out, and_8_out, soma_sub4bits_1_s, soma_sub4bits_2_s;

  and and_1 (and_4_out[3], not_1_out, A[3]);
  not not_1 (not_1_out, A_B);
  and and_2 (and_4_out[2], not_1_out, A[2]);
  and and_3 (and_4_out[1], not_1_out, A[1]);
  Soma_Sub4bits soma_sub4bits_1 (
    .\Soma_Subtração (1'b0), .A(and_4_out), .B(4'b0001), .S(soma_sub4bits_1_s));  // open: Carry_Out
  and and_4 (and_4_out[0], not_1_out, A[0]);
  and and_5 (and_8_out[3], A_B, B[3]);
  and and_6 (and_8_out[2], A_B, B[2]);
  OR or_1 (.A(soma_sub4bits_1_s), .B(soma_sub4bits_2_s), .OR(plus_1));
  and and_7 (and_8_out[1], A_B, B[1]);
  and and_8 (and_8_out[0], A_B, B[0]);
  Soma_Sub4bits soma_sub4bits_2 (
    .\Soma_Subtração (1'b0), .A(and_8_out), .B(4'b0001), .S(soma_sub4bits_2_s));  // open: Carry_Out

  // Notes on the sheet:
  //   Andre Sulivam - 391998
endmodule

module Decremento (
  input  A_B,
  input  [3:0] A,
  input  [3:0] B,
  output [3:0] minus_1
);

  wire not_1_out;
  wire [3:0] and_4_out, and_8_out, soma_sub4bits_1_s, soma_sub4bits_2_s;

  and and_1 (and_4_out[3], not_1_out, A[3]);
  not not_1 (not_1_out, A_B);
  and and_2 (and_4_out[2], not_1_out, A[2]);
  and and_3 (and_4_out[1], not_1_out, A[1]);
  Soma_Sub4bits soma_sub4bits_1 (
    .\Soma_Subtração (1'b1), .A(and_4_out), .B(4'b0001), .S(soma_sub4bits_1_s));  // open: Carry_Out
  and and_4 (and_4_out[0], not_1_out, A[0]);
  and and_5 (and_8_out[2], A_B, B[2]);
  and and_6 (and_8_out[3], A_B, B[3]);
  OR or_1 (.A(soma_sub4bits_1_s), .B(soma_sub4bits_2_s), .OR(minus_1));
  and and_7 (and_8_out[1], A_B, B[1]);
  and and_8 (and_8_out[0], A_B, B[0]);
  Soma_Sub4bits soma_sub4bits_2 (
    .\Soma_Subtração (1'b1), .A(and_8_out), .B(4'b0001), .S(soma_sub4bits_2_s));  // open: Carry_Out

  // Notes on the sheet:
  //   Andre Sulivam - 391998
endmodule

module Produto (
  input  [3:0] A,
  input  [3:0] B,
  input  _2A_2B,
  output [3:0] Produto
);

  wire [3:0] multiplexer_1_out;

  Multiplexer #(.select(1), .width(4)) multiplexer_1 (.in0(A), .in1(B), .out(multiplexer_1_out), .sel(_2A_2B));
  Soma_Sub4bits soma_sub4bits_1 (
    .\Soma_Subtração (1'b0), .A(multiplexer_1_out), .B(multiplexer_1_out), .S(Produto));  // open: Carry_Out

  // Notes on the sheet:
  //   Andre Sulivam - 391998
endmodule
