// Logisim project Guia07.circ as structural Verilog: 15 circuits, main circuit ULA
module meiaSoma (
  input  a,
  input  b,
  output carryOut,
  output soma
);

  and and_1 (carryOut, b, a);
  xor xor_1 (soma, a, b);
endmodule

module somaCompleta (
  input  a,
  input  b,
  input  carryIn,
  output carryOut,
  output s0
);

  wire meiasoma_1_carryout, meiasoma_1_soma, meiasoma_2_carryout;

  or or_1 (carryOut, meiasoma_1_carryout, meiasoma_2_carryout);
  meiaSoma meiasoma_1 (.carryOut(meiasoma_1_carryout), .a(a), .b(b), .soma(meiasoma_1_soma));
  meiaSoma meiasoma_2 (.carryOut(meiasoma_2_carryout), .a(meiasoma_1_soma), .b(carryIn), .soma(s0));
endmodule

module somaAlgebrica__4bits (
  input  [3:0] fator2,
  input  [3:0] fator1,
  input  _0___soma,
  output [3:0] Resultado
);

  wire somacompleta_2_carryout, somacompleta_3_carryout, somacompleta_4_carryout, xor_1_out, xor_2_out,
       xor_3_out, xor_4_out;

  xor xor_1 (xor_1_out, fator2[3], _0___soma);
  somaCompleta somacompleta_1 (
    .a(xor_1_out), .b(fator1[3]), .s0(Resultado[3]), .carryIn(somacompleta_2_carryout));  // open: carryOut
  xor xor_2 (xor_2_out, fator2[2], _0___soma);
  somaCompleta somacompleta_2 (
    .carryOut(somacompleta_2_carryout), .a(xor_2_out), .b(fator1[2]), .s0(Resultado[2]),
    .carryIn(somacompleta_3_carryout));
  xor xor_3 (xor_3_out, fator2[1], _0___soma);
  somaCompleta somacompleta_3 (
    .carryOut(somacompleta_3_carryout), .a(xor_3_out), .b(fator1[1]), .s0(Resultado[1]),
    .carryIn(somacompleta_4_carryout));
  xor xor_4 (xor_4_out, fator2[0], _0___soma);
  somaCompleta somacompleta_4 (
    .carryOut(somacompleta_4_carryout), .a(xor_4_out), .b(fator1[0]), .s0(Resultado[0]), .carryIn(_0___soma));

  // Notes on the sheet:
  //   1 - subtrai
endmodule

module comparador__4bits (
  input  [3:0] in_1,
  input  [3:0] in_2,
  output out_3
);

  wire [3:0] xnor_1_out;

  assign xnor_1_out = ~(in_1 ^ in_2);  // XNOR_Gate xnor_1, 4 bits wide
  and and_1 (out_3, xnor_1_out[3], xnor_1_out[2], xnor_1_out[1], xnor_1_out[0]);

  // Notes on the sheet:
  //   Comparador Lógico
endmodule

module ULA (
  input  [3:0] fator1,
  input  [3:0] fator2,
  input  operacao,
  output [3:0] \and ,
  output [3:0] \or ,
  output [3:0] resultado,
  output menor,
  output maior,
  output igual,
  output [3:0] complemento_de_1,
  output [3:0] incremento_de_1,
  output [3:0] complemento_de_2,
  output [3:0] decremento_de_1,
  output [3:0] produto_2
);

  ParteLogica partelogica_1 (.fator1(fator1), .fator2(fator2), .And(\and ), .Or(\or ));
  ParteAritimetica partearitimetica_1 (
    .fator1(fator1), .fator2(fator2), .operacao(operacao), .Resultado(resultado), .menor(menor),
    .maior(maior), .igual(igual));
  Operacoes operacoes_1 (
    .in(fator2), .complemento_de_1(complemento_de_1), .Incremento_de_1(incremento_de_1),
    .Complemento_de_2(complemento_de_2), .Decremento_de_1(decremento_de_1), .Produto_de_2(produto_2));

  // Notes on the sheet:
  //   Unidade Lógica Aritimética
endmodule

module Comparador_Aritmetico (
  input  [3:0] fator1,
  input  [3:0] fator2,
  output menor,
  output maior,
  output igual
);

  wire [2:0] somaalgebrica_4bits_1_resultado;

  somaAlgebrica__4bits somaalgebrica_4bits_1 (
    .fator2(fator2), .fator1(fator1), .Resultado({menor, somaalgebrica_4bits_1_resultado}), ._0___soma(1'b1));
  comparador__4bits comparador_4bits_1 (.in_1(fator1), .in_2(fator2), .out_3(igual));
  nor nor_1 (maior, menor, igual);

  // Notes on the sheet:
  //   Comparador Aritimético
endmodule

module logica (
  input  [3:0] a,
  input  [3:0] b,
  output [3:0] \and ,
  output [3:0] \or 
);

  assign \and  = a & b;  // AND_Gate and_1, 4 bits wide
  assign \or  = a | a;  // OR_Gate or_1, 4 bits wide

  // Notes on the sheet:
  //   Lógica
endmodule

module Complemento1 (
  input  [3:0] in,
  output [3:0] out
);

  assign out = ~in;  // NOT_Gate not_1, 4 bits wide

  // Notes on the sheet:
  //   Complemento de 1
endmodule

module Complemento2 (
  input  [3:0] in,
  output [3:0] C2
);

  wire [3:0] complemento1_1_out;

  Complemento1 complemento1_1 (.in(in), .out(complemento1_1_out));
  Incremento1 incremento1_1 (.in(complemento1_1_out), .incremento(C2));

  // Notes on the sheet:
  //   Complemento de 2
endmodule

module Incremento1 (
  input  [3:0] in,
  output [3:0] incremento
);

  somaAlgebrica__4bits somaalgebrica_4bits_1 (.fator2(in), .fator1(4'b0001), .Resultado(incremento), ._0___soma(1'b0));

  // Notes on the sheet:
  //   Incremento de 1
endmodule

module Decremento1 (
  input  [3:0] in,
  output [3:0] incremento
);

  somaAlgebrica__4bits somaalgebrica_4bits_1 (.fator2(4'b0001), .fator1(in), .Resultado(incremento), ._0___soma(1'b1));

  // Notes on the sheet:
  //   Incremento de 1
endmodule

module Produto2 (
  input  [3:0] in,
  output [3:0] Produto_2
);

  somaAlgebrica__4bits somaalgebrica_4bits_1 (.fator2(in), .fator1(in), .Resultado(Produto_2), ._0___soma(1'b0));

  // Notes on the sheet:
  //   Produto 2
endmodule

module ParteLogica (
  input  [3:0] fator1,
  input  [3:0] fator2,
  output [3:0] And,
  output [3:0] Or
);

  logica logica_1 (.a(fator1), .b(fator2), .\and (And), .\or (Or));
endmodule

module ParteAritimetica (
  input  [3:0] fator1,
  input  [3:0] fator2,
  input  operacao,
  output [3:0] Resultado,
  output menor,
  output maior,
  output igual
);

  Comparador_Aritmetico comparador_aritmetico_1 (
    .fator1(fator2), .fator2(fator1), .menor(menor), .maior(maior), .igual(igual));
  somaAlgebrica__4bits somaalgebrica_4bits_1 (
    .fator2(fator1), .fator1(fator2), .Resultado(Resultado), ._0___soma(operacao));
endmodule

module Operacoes (
  input  [3:0] in,
  output [3:0] complemento_de_1,
  output [3:0] Incremento_de_1,
  output [3:0] Complemento_de_2,
  output [3:0] Decremento_de_1,
  output [3:0] Produto_de_2
);

  Complemento1 complemento1_1 (.in(in), .out(complemento_de_1));
  Incremento1 incremento1_1 (.in(in), .incremento(Incremento_de_1));
  Complemento2 complemento2_1 (.in(in), .C2(Complemento_de_2));
  Decremento1 decremento1_1 (.in(in), .incremento(Decremento_de_1));
  Produto2 produto2_1 (.in(in), .Produto_2(Produto_de_2));
endmodule
