// Logisim project ALU.circ as structural Verilog
module Comparador (
  input  a3,
  input  b3,
  input  a2,
  input  b2,
  input  a1,
  input  b1,
  input  a0,
  input  b0,
  output a_b,
  output a_b_2,
  output a_b_3,
  output a__b
);

  wire and_1_out, and_2_out, and_3_out, and_4_out, and_5_out, and_6_out, and_7_out, and_8_out, and_9_out,
       and_10_out, and_11_out, and_12_out, and_13_out, and_14_out, nor_1_out, nor_2_out, nor_3_out,
       nor_4_out, not_1_out, not_2_out, not_3_out, not_4_out, not_5_out, not_6_out, not_7_out, not_8_out;

  not not_1 (not_1_out, a3);
  not not_2 (not_2_out, b3);
  not not_3 (not_3_out, a2);
  not not_4 (not_4_out, b2);
  not not_5 (not_5_out, a1);
  not not_6 (not_6_out, b1);
  not not_7 (not_7_out, a0);
  not not_8 (not_8_out, b0);
  and and_1 (and_1_out, not_1_out, b3);
  and and_2 (and_2_out, a3, not_2_out);
  and and_3 (and_3_out, not_3_out, b2);
  and and_4 (and_4_out, a2, not_4_out);
  and and_5 (and_5_out, not_5_out, b1);
  and and_6 (and_6_out, a1, not_6_out);
  and and_7 (and_7_out, not_7_out, b0);
  and and_8 (and_8_out, a0, not_8_out);
  nor nor_1 (nor_1_out, and_1_out, and_2_out);
  nor nor_2 (nor_2_out, and_3_out, and_4_out);
  nor nor_3 (nor_3_out, and_5_out, and_6_out);
  nor nor_4 (nor_4_out, and_7_out, and_8_out);
  and and_9 (and_9_out, nor_1_out, and_3_out);
  and and_10 (and_10_out, nor_1_out, and_4_out);
  and and_11 (and_11_out, nor_1_out, and_5_out, nor_2_out);
  and and_12 (and_12_out, nor_1_out, and_6_out, nor_2_out);
  and and_13 (and_13_out, nor_1_out, and_7_out, nor_2_out, nor_3_out);
  and and_14 (and_14_out, nor_1_out, and_8_out, nor_2_out, nor_3_out);
  and and_15 (a_b_3, nor_1_out, nor_2_out, nor_3_out, nor_4_out);
  or or_1 (a_b, and_1_out, and_9_out, and_11_out, and_13_out);
  or or_2 (a_b_2, and_2_out, and_10_out, and_12_out, and_14_out);
  not not_9 (a__b, a_b_3);
endmodule

module Half_Adder (
  input  x,
  input  y,
  output s0,
  output Carry_Out
);

  wire not_1_out, or_1_out;

  or or_1 (or_1_out, y, x);
  and and_1 (Carry_Out, x, y);
  not not_1 (not_1_out, Carry_Out);
  and and_2 (s0, or_1_out, not_1_out);
endmodule

module FA (
  input  carry,
  input  x,
  input  y,
  output s0,
  output Carry_out
);

  wire half_adder_1_carry_out, half_adder_2_carry_out, half_adder_2_s0;

  Half_Adder half_adder_1 (.x(carry), .y(half_adder_2_s0), .s0(s0), .Carry_Out(half_adder_1_carry_out));
  Half_Adder half_adder_2 (.x(x), .y(y), .s0(half_adder_2_s0), .Carry_Out(half_adder_2_carry_out));
  or or_1 (Carry_out, half_adder_1_carry_out, half_adder_2_carry_out);
endmodule

module ALU (
  input  a0,
  input  b0,
  input  a1,
  input  b1,
  input  a2,
  input  b2,
  input  a3,
  input  b3,
  input  op,
  output s0,
  output s1,
  output s2,
  output s3,
  output s4,
  output Zero,
  output Overflow,
  output A___B,
  output A___B_2,
  output A___B_3,
  output A____B
);

  wire fa_1_carry_out, fa_2_carry_out, fa_3_carry_out, fa_4_carry_out, xor_1_out, xor_2_out, xor_3_out,
       xor_4_out;

  xor xor_1 (xor_1_out, b0, op);
  xor xor_2 (xor_2_out, b1, op);
  xor xor_3 (xor_3_out, b2, op);
  xor xor_4 (xor_4_out, b3, op);
  FA fa_1 (.carry(op), .x(a0), .y(xor_1_out), .s0(s0), .Carry_out(fa_1_carry_out));
  FA fa_2 (.carry(fa_1_carry_out), .x(a1), .y(xor_2_out), .s0(s1), .Carry_out(fa_2_carry_out));
  FA fa_3 (.carry(fa_2_carry_out), .x(a2), .y(xor_3_out), .s0(s2), .Carry_out(fa_3_carry_out));
  FA fa_4 (.carry(fa_3_carry_out), .x(a3), .y(xor_4_out), .s0(s3), .Carry_out(fa_4_carry_out));
  xor xor_5 (s4, fa_4_carry_out, op);
  Comparador comparador_1 (
    .a3(a3), .b3(xor_4_out), .a2(a2), .b2(xor_3_out), .a1(a1), .b1(xor_2_out), .a0(a0), .b0(xor_1_out),
    .a_b(A___B), .a_b_2(A___B_2), .a_b_3(A___B_3), .a__b(A____B));
  Zero zero_1 (.s0(s0), .s1(s1), .s2(s2), .s3(s3), .s4(s4), .Zero(Zero));
  Overflow overflow_1 (.c4(fa_3_carry_out), .s4(s4), .Overflow(Overflow));

  // Notes on the sheet:
  //   0 - Adição
  //   1 - Subtração
endmodule

module Overflow (
  input  c4,
  input  s4,
  output Overflow
);

  wire not_1_out;

  not not_1 (not_1_out, c4);
  and and_1 (Overflow, not_1_out, s4);
endmodule

module Zero (
  input  s0,
  input  s1,
  input  s2,
  input  s3,
  input  s4,
  output Zero
);

  nor nor_1 (Zero, s0, s1, s2, s3, s4);
endmodule

module Incremento_de_1 (
  input  [3:0] in_1,
  output [3:0] out_2
);

  wire half_adder_1_carry_out, half_adder_2_carry_out, half_adder_3_carry_out;

  Half_Adder half_adder_1 (.x(1'b1), .y(in_1[0]), .s0(out_2[0]), .Carry_Out(half_adder_1_carry_out));
  Half_Adder half_adder_2 (.x(half_adder_1_carry_out), .y(in_1[1]), .s0(out_2[1]), .Carry_Out(half_adder_2_carry_out));
  Half_Adder half_adder_3 (.x(half_adder_2_carry_out), .y(in_1[2]), .s0(out_2[2]), .Carry_Out(half_adder_3_carry_out));
  Half_Adder half_adder_4 (.x(half_adder_3_carry_out), .y(in_1[3]), .s0(out_2[3]));  // open: Carry_Out
endmodule

module ALU_GUIA7 (
  input  [3:0] A,
  input  [3:0] B,
  input  op,
  output [4:0] out_4,
  output Zero,
  output Overflow,
  output A___B,
  output A___B_2,
  output A____B,
  output A____B_2,
  output [3:0] Complemento_de_1,
  output [3:0] Complemento_de_2,
  output [3:0] Incremento_de_1
);

  assign Complemento_de_1 = ~B;  // NOT_Gate not_1, 4 bits wide
  ALU alu_1 (
    .a0(A[0]), .b0(B[0]), .a1(A[1]), .b1(B[1]), .a2(A[2]), .b2(B[2]), .a3(A[3]), .b3(B[3]), .op(op),
    .s0(out_4[0]), .s1(out_4[1]), .s2(out_4[2]), .s3(out_4[3]), .s4(out_4[4]), .Zero(Zero),
    .Overflow(Overflow), .A___B(A___B), .A___B_2(A___B_2), .A___B_3(A____B), .A____B(A____B_2));
  Incremento_de_1 incremento_de_1_1 (.in_1(Complemento_de_1), .out_2(Complemento_de_2));
  Incremento_de_1 incremento_de_1_2 (.in_1(B), .out_2(Incremento_de_1));

  // Notes on the sheet:
  //   0 - Adição
  //   1 - Subtração
endmodule
