// Logisim project guia_07.circ as structural Verilog: 6 circuits, main circuit main
module main (
  input  comp1,
  input  a0,
  input  a1,
  input  a2,
  input  a3,
  output out_6,
  output out_7,
  output out_8,
  output out_9,
  output out_10,
  output out_11,
  output out_12,
  output out_13,
  output out_14,
  output out_15,
  output out_16,
  output out_17,
  output out_18,
  output out_19
);

  ex_01 ex_01_1 (
    .a0(a0), .a1(a1), .a2(a2), .a3(a3), .complemento(comp1), .out_6(out_6), .out_7(out_7), .out_8(out_8),
    .out_9(out_9));
  ex_02 ex_02_1 (
    .a0(a0), .a1(a1), .a2(a2), .a3(a3), .complemento(comp1), .s0(out_10), .s1(out_11), .s2(out_12),
    .s3(out_13), .s4(out_14));
  ex_03 ex_03_1 (
    .a0(a0), .a1(a1), .a2(a2), .a3(a3), .complemento(comp1), .s0(out_15), .s1(out_16), .s2(out_17),
    .s3(out_18), .s4(out_19));
endmodule

module ex_01 (
  input  a0,
  input  a1,
  input  a2,
  input  a3,
  input  complemento,
  output out_6,
  output out_7,
  output out_8,
  output out_9
);

  xor xor_1 (out_6, a0, complemento);
  xor xor_2 (out_7, complemento, a1);
  xor xor_3 (out_8, a2, complemento);
  xor xor_4 (out_9, complemento, a3);
endmodule

module ex_02 (
  input  a0,
  input  a1,
  input  a2,
  input  a3,
  input  complemento,
  output s0,
  output s1,
  output s2,
  output s3,
  output s4
);

  wire ex_01_1_out_6, ex_01_1_out_7, ex_01_1_out_8, ex_01_1_out_9, half_adder_1_s1, half_adder_2_s1,
       half_adder_3_s1;

  ex_01 ex_01_1 (
    .a0(a0), .a1(a1), .a2(a2), .a3(a3), .complemento(complemento), .out_6(ex_01_1_out_6),
    .out_7(ex_01_1_out_7), .out_8(ex_01_1_out_8), .out_9(ex_01_1_out_9));
  half_adder half_adder_1 (.x(complemento), .y(ex_01_1_out_6), .s0(s0), .s1(half_adder_1_s1));
  half_adder half_adder_2 (.x(half_adder_1_s1), .y(ex_01_1_out_7), .s0(s1), .s1(half_adder_2_s1));
  half_adder half_adder_3 (.x(half_adder_2_s1), .y(ex_01_1_out_8), .s0(s2), .s1(half_adder_3_s1));
  half_adder half_adder_4 (.x(half_adder_3_s1), .y(ex_01_1_out_9), .s0(s3), .s1(s4));
endmodule

module half_adder (
  input  x,
  input  y,
  output s0,
  output s1
);

  xor xor_1 (s0, x, y);
  and and_1 (s1, x, y);
endmodule

module ex_03 (
  input  a0,
  input  a1,
  input  a2,
  input  a3,
  input  complemento,
  output s0,
  output s1,
  output s2,
  output s3,
  output s4
);

  wire ex_01_1_out_6, ex_01_1_out_7, ex_01_1_out_8, ex_01_1_out_9, half_sub_1_b_out, half_sub_2_b_out,
       half_sub_3_b_out;

  ex_01 ex_01_1 (
    .a0(a0), .a1(a1), .a2(a2), .a3(a3), .complemento(complemento), .out_6(ex_01_1_out_6),
    .out_7(ex_01_1_out_7), .out_8(ex_01_1_out_8), .out_9(ex_01_1_out_9));
  half_sub half_sub_1 (.y(complemento), .x(ex_01_1_out_6), .s0(s0), .b_out(half_sub_1_b_out));
  half_sub half_sub_2 (.y(half_sub_1_b_out), .x(ex_01_1_out_7), .s0(s1), .b_out(half_sub_2_b_out));
  half_sub half_sub_3 (.y(half_sub_2_b_out), .x(ex_01_1_out_8), .s0(s2), .b_out(half_sub_3_b_out));
  half_sub half_sub_4 (.y(half_sub_3_b_out), .x(ex_01_1_out_9), .s0(s3), .b_out(s4));
endmodule

module half_sub (
  input  y,
  input  x,
  output s0,
  output b_out
);

  wire not_1_out;

  not not_1 (not_1_out, x);
  xor xor_1 (s0, y, x);
  and and_1 (b_out, not_1_out, y);
endmodule
