// Logisim project Guia07.circ as structural Verilog: 6 circuits, main circuit Full_Adder
module Full_Adder (
  input  Cin,
  input  A,
  input  B,
  output s0,
  output Cout
);

  wire half_adder2_1_s3, half_adder_1_s4, half_adder_1_s5;

  Half_Adder half_adder_1 (.x(A), .y(B), .s4(half_adder_1_s4), .s5(half_adder_1_s5));
  Half_Adder2 half_adder2_1 (.Vai_um(Cin), .x(half_adder_1_s4), .s2(s0), .s3(half_adder2_1_s3));
  or or_1 (Cout, half_adder2_1_s3, half_adder_1_s5);
endmodule

module Half_Adder (
  input  x,
  input  y,
  output s4,
  output s5
);

  xor xor_1 (s4, x, y);
  and and_1 (s5, y, x);
endmodule

module Half_Adder2 (
  input  Vai_um,
  input  x,
  output s2,
  output s3
);

  xor xor_1 (s2, Vai_um, x);
  and and_1 (s3, x, Vai_um);
endmodule

module ALU_4bits_1 (
  input  in_1,
  input  in_2,
  input  in_3,
  input  in_4,
  input  Cin,
  input  A0,
  input  B0,
  input  A1,
  input  B1,
  input  A2,
  input  B2,
  input  A3,
  input  B3,
  output s0,
  output s1,
  output s2,
  output s3,
  output Cout,
  output Overflow,
  output zero
);

  wire and_1_out, and_2_out, and_3_out, and_4_out, full_adder_1_cout, full_adder_1_s0, full_adder_2_cout,
       full_adder_2_s0, full_adder_3_cout, full_adder_3_s0, full_adder_4_s0, or_1_out, or_2_out, or_3_out,
       or_4_out, xor_1_out, xor_2_out, xor_3_out, xor_4_out, xor_5_out, xor_6_out, xor_7_out, xor_8_out;

  xor xor_1 (xor_1_out, B2, Cin);
  Full_Adder full_adder_1 (.Cin(Cin), .A(A0), .B(xor_2_out), .s0(full_adder_1_s0), .Cout(full_adder_1_cout));
  xor xor_2 (xor_2_out, B0, Cin);
  Full_Adder full_adder_2 (
    .Cin(full_adder_1_cout), .A(A1), .B(xor_3_out), .s0(full_adder_2_s0), .Cout(full_adder_2_cout));
  xor xor_3 (xor_3_out, B1, Cin);
  Full_Adder full_adder_3 (
    .Cin(full_adder_2_cout), .A(A2), .B(xor_1_out), .s0(full_adder_3_s0), .Cout(full_adder_3_cout));
  and and_1 (and_1_out, A3, B3);
  Full_Adder full_adder_4 (.Cin(full_adder_3_cout), .A(A3), .B(xor_4_out), .s0(full_adder_4_s0), .Cout(Cout));
  or or_1 (or_1_out, A3, B3);
  xor xor_4 (xor_4_out, B3, Cin);
  xor xor_5 (xor_5_out, A0, B0);
  and and_2 (and_2_out, A0, B0);
  or or_2 (or_2_out, A0, B0);
  xor xor_6 (xor_6_out, A1, B1);
  and and_3 (and_3_out, A1, B1);
  or or_3 (or_3_out, A1, B1);
  xor xor_7 (xor_7_out, A2, B2);
  and and_4 (and_4_out, A2, B2);
  or or_4 (or_4_out, A2, B2);
  xor xor_8 (xor_8_out, A3, B3);
  Multiplexer #(.select(3), .width(1)) multiplexer_1 (
    .in0(and_2_out), .in1(full_adder_1_s0), .in2(or_2_out), .in3(xor_5_out), .out(s0),
    .sel({in_3, in_2, in_1}));  // open: in4, in5, in6, in7
  Multiplexer #(.select(3), .width(1)) multiplexer_2 (
    .in0(and_3_out), .in1(full_adder_2_s0), .in2(or_3_out), .in3(xor_6_out), .out(s1),
    .sel({in_3, in_2, in_1}));  // open: in4, in5, in6, in7
  Multiplexer #(.select(3), .width(1)) multiplexer_3 (
    .in0(and_4_out), .in1(full_adder_3_s0), .in2(or_4_out), .in3(xor_7_out), .out(s2),
    .sel({in_3, in_2, in_1}));  // open: in4, in5, in6, in7
  Multiplexer #(.select(3), .width(1)) multiplexer_4 (
    .in0(and_1_out), .in1(full_adder_4_s0), .in2(or_1_out), .in3(xor_8_out), .out(s3),
    .sel({in_3, in_2, in_1}));  // open: in4, in5, in6, in7
  xor xor_9 (Overflow, Cout, Cin);
  xor xor_10 (zero, full_adder_4_s0, Overflow);
endmodule

module Comparator (
  input  a1,
  input  a0,
  input  b1,
  input  b0,
  output s,
  output s1
);

  wire and_1_out, and_2_out, and_3_out, and_4_out, and_5_out, and_6_out, not_1_out, not_2_out, not_3_out,
       not_4_out;

  not not_1 (not_1_out, b1);
  not not_2 (not_2_out, b0);
  not not_3 (not_3_out, a1);
  not not_4 (not_4_out, a0);
  and and_1 (and_1_out, b1, not_3_out);
  and and_2 (and_2_out, b0, not_4_out, not_3_out);
  and and_3 (and_3_out, not_4_out, b0, b1);
  and and_4 (and_4_out, a1, a0, not_2_out);
  and and_5 (and_5_out, not_1_out, a1);
  and and_6 (and_6_out, a0, not_1_out, not_2_out);
  or or_1 (s1, and_1_out, and_2_out, and_3_out);
  or or_2 (s, and_4_out, and_5_out, and_6_out);
endmodule

module ALU_4bits_2 (
  input  Op1,
  input  _2,
  input  Op3,
  input  Op4,
  input  Cin,
  input  A0,
  input  B0,
  input  A1,
  input  B1,
  input  A2,
  input  B2,
  input  A3,
  input  B3,
  output s0,
  output s1,
  output s2,
  output s3,
  output s4,
  output Overflow,
  output Zero
);

  ALU_4bits_1 alu_4bits_1_1 (
    .Cin(Cin), .A0(A0), .B0(B0), .A1(A1), .B1(B1), .A2(A2), .B2(B2), .A3(A3), .B3(B3), .in_1(Op1), .in_2(_2),
    .in_3(Op3), .in_4(Op4), .s0(s0), .s1(s1), .s2(s2), .s3(s3), .Cout(s4), .Overflow(Overflow), .zero(Zero));
endmodule
