// Logisim project guia 07.circ as structural Verilog
module meia_soma (
  input  a,
  input  b,
  output s0,
  output s1
);

  and and_1 (s1, a, b);
  xor xor_1 (s0, a, b);

  // Notes on the sheet:
  //   Meia soma
endmodule

module soma_completa (
  input  c,
  input  a,
  input  b,
  output s0,
  output s1
);

  wire meia_soma_1_s0, meia_soma_1_s1, meia_soma_2_s1;

  meia_soma meia_soma_1 (.a(a), .b(b), .s0(meia_soma_1_s0), .s1(meia_soma_1_s1));
  meia_soma meia_soma_2 (.a(c), .b(meia_soma_1_s0), .s0(s0), .s1(meia_soma_2_s1));
  or or_1 (s1, meia_soma_2_s1, meia_soma_1_s1);
endmodule

module soma_completa_4bits (
  input  [3:0] in_1,
  input  [3:0] in_2,
  output [3:0] out_3
);

  wire meia_soma_1_s1, soma_completa_1_s1, soma_completa_2_s1;

  meia_soma meia_soma_1 (.a(in_1[0]), .b(in_2[0]), .s0(out_3[0]), .s1(meia_soma_1_s1));
  soma_completa soma_completa_1 (.c(meia_soma_1_s1), .a(in_1[1]), .b(in_2[1]), .s0(out_3[1]), .s1(soma_completa_1_s1));
  soma_completa soma_completa_2 (
    .c(soma_completa_1_s1), .a(in_1[2]), .b(in_2[2]), .s0(out_3[2]), .s1(soma_completa_2_s1));
  soma_completa soma_completa_3 (.c(soma_completa_2_s1), .a(in_1[3]), .b(in_2[3]), .s0(out_3[3]));  // open: s1
endmodule

module \meia_diferença  (
  input  a,
  input  b,
  output s0,
  output s1
);

  wire not_1_out;

  not not_1 (not_1_out, a);
  and and_1 (s1, not_1_out, b);
  xor xor_1 (s0, a, b);
endmodule

module \diferença_completa  (
  input  in_1,
  input  in_2,
  input  in_3,
  output out_4,
  output out_5
);

  wire and_1_out, and_2_out, not_1_out, not_2_out, xor_1_out;

  not not_1 (not_1_out, in_2);
  xor xor_1 (xor_1_out, in_2, in_3);
  and and_1 (and_1_out, not_1_out, in_3);
  not not_2 (not_2_out, xor_1_out);
  xor xor_2 (out_4, in_1, xor_1_out);
  and and_2 (and_2_out, in_1, not_2_out);
  or or_1 (out_5, and_2_out, and_1_out);
endmodule

module \diferença_completa_4bits  (
  input  [3:0] in_1,
  input  [3:0] in_2,
  output [3:0] out_3
);

  wire \diferença_completa_1_out_5 , \diferença_completa_2_out_5 , \meia_diferença_1_s1 ;

  \meia_diferença  \meia_diferença_1  (.a(in_1[0]), .b(in_2[0]), .s0(out_3[0]), .s1(\meia_diferença_1_s1 ));
  \diferença_completa  \diferença_completa_1  (
    .in_1(\meia_diferença_1_s1 ), .in_2(in_1[1]), .in_3(in_2[1]), .out_4(out_3[1]),
    .out_5(\diferença_completa_1_out_5 ));
  \diferença_completa  \diferença_completa_2  (
    .in_1(\diferença_completa_1_out_5 ), .in_2(in_1[2]), .in_3(in_2[2]), .out_4(out_3[2]),
    .out_5(\diferença_completa_2_out_5 ));
  \diferença_completa  \diferença_completa_3  (
    .in_1(\diferença_completa_2_out_5 ), .in_2(in_1[3]), .in_3(in_2[3]), .out_4(out_3[3]));  // open: out_5
endmodule

module complemeto_de_um (
  input  [3:0] in_1,
  output [3:0] out_2
);

  assign out_2 = ~in_1;  // NOT_Gate not_1, 4 bits wide
endmodule

module encremento (
  input  [3:0] in_1,
  output [3:0] out_2
);

  soma_completa_4bits soma_completa_4bits_1 (.in_1(4'b0001), .in_2(in_1), .out_3(out_2));
endmodule

module complementode2 (
  input  [3:0] in_1,
  output [3:0] out_2
);

  wire [3:0] not_1_out;

  assign not_1_out = ~in_1;  // NOT_Gate not_1, 4 bits wide
  encremento encremento_1 (.in_1(not_1_out), .out_2(out_2));
endmodule

module decrementar1 (
  input  [3:0] in_1,
  output [3:0] out_2
);

  \diferença_completa_4bits  \diferença_completa_4bits_1  (.in_1(in_1), .in_2(4'b0001), .out_3(out_2));
endmodule

module produtopor2 (
  input  [3:0] in_1,
  output [3:0] out_2
);

  soma_completa_4bits soma_completa_4bits_1 (.in_1(in_1), .in_2(in_1), .out_3(out_2));
endmodule

module ULA (
  input  [3:0] a,
  input  [3:0] b,
  output [3:0] soma,
  output [3:0] out_4,
  output [3:0] out_5,
  output [3:0] out_6,
  output [3:0] out_7,
  output [3:0] out_8,
  output [3:0] out_9
);

  soma_completa_4bits soma_completa_4bits_1 (.in_1(a), .in_2(b), .out_3(soma));
  \diferença_completa_4bits  \diferença_completa_4bits_1  (.in_1(a), .in_2(b), .out_3(out_4));
  complemeto_de_um complemeto_de_um_1 (.in_1(b), .out_2(out_5));
  encremento encremento_1 (.in_1(b), .out_2(out_6));
  complementode2 complementode2_1 (.in_1(b), .out_2(out_7));
  decrementar1 decrementar1_1 (.in_1(b), .out_2(out_8));
  produtopor2 produtopor2_1 (.in_1(b), .out_2(out_9));

  // Notes on the sheet:
  //   U L A
  //                 subtraçao
  //                 complemento de 1
  //   encremento de 1
  //   complemento de 2
  //   decremento de 1
  //   produto por 2
  //   Mariana do Amaral
  //   405819
endmodule
