// Logisim project ALU_4BITS.circ as structural Verilog: 14 circuits, main circuit half_adder
module main (
  input  [3:0] A,
  input  [3:0] B,
  output [3:0] complemento_de_2_de_A,
  output [3:0] complemento_de_2_de_B,
  output ZERO_NA_SOMA,
  output A_OU_B_ZERO,
  output ZERO_NA_SUBTRACAO,
  output OVERFLOW,
  output CARRY,
  output DIFERENTE,
  output A___B,
  output [3:0] complemento_de_1_de_A,
  output [3:0] complemento_de_1_de_B,
  output [3:0] incremento_de_1_de_A,
  output [3:0] incremento_de_1_de_B,
  output [3:0] decremento_de_1_de_A,
  output [3:0] decremento_de_1_de_B,
  output [3:0] A___B_2,
  output [3:0] A___B_3,
  output produto_de_2_por_A_errado,
  output [3:0] produto_por_2_de_A,
  output produto_de_2_por_B_errado,
  output [3:0] produto_por_2_de_B
);

  ALU_4bits alu_4bits_1 (
    .a3(A[3]), .a2(A[2]), .a1(A[1]), .a0(A[0]), .b3(B[3]), .b2(B[2]), .b1(B[1]), .b0(B[0]), .SOMA(A___B_3),
    .produto_por_2_de_A(produto_por_2_de_A), .produto_por_2_de_B(produto_por_2_de_B), .A___B(A___B_2),
    .complemento_de_1_de_B(complemento_de_1_de_B), .complemento_de_1_de_A(complemento_de_1_de_A),
    .produto_de_A_errado(produto_de_2_por_A_errado), .produto_de_B_errado(produto_de_2_por_B_errado),
    .ZERO_NA_SOMA(ZERO_NA_SOMA), .OVERFLOW(OVERFLOW), .CARRY(CARRY), .A_OU_B_ZERO(A_OU_B_ZERO),
    .DIFERENTE(DIFERENTE), .ZERO_NA_SUBTRACAO(ZERO_NA_SUBTRACAO), .A___B_2(A___B),
    .complemento_de_2_de_A(complemento_de_2_de_A), .complemento_de_2_de_B(complemento_de_2_de_B),
    .incremento_de_1_de_A(incremento_de_1_de_A), .incremento_de_1_de_B(incremento_de_1_de_B),
    .decremento_de_1_de_A(decremento_de_1_de_A), .decremento_de_1_de_B(decremento_de_1_de_B));
endmodule

module half_adder (
  input  A,
  input  B,
  output S0,
  output S1
);

  xor xor_1 (S0, A, B);
  and and_1 (S1, A, B);
endmodule

module full_adder (
  input  A,
  input  B,
  input  C,
  output S0,
  output S1
);

  wire half_adder_1_s0, half_adder_1_s1, half_adder_2_s1;

  half_adder half_adder_1 (.A(A), .B(B), .S0(half_adder_1_s0), .S1(half_adder_1_s1));
  half_adder half_adder_2 (.A(half_adder_1_s0), .B(C), .S0(S0), .S1(half_adder_2_s1));
  or or_1 (S1, half_adder_2_s1, half_adder_1_s1);

  // Notes on the sheet:
  //   meia-soma
  //   meia-soma
endmodule

module haf_subtractor (
  input  A,
  input  B,
  output S0,
  output S1
);

  wire and_1_out, and_2_out, not_1_out, not_2_out, not_3_out;

  not not_1 (not_1_out, A);
  not not_2 (not_2_out, B);
  not not_3 (not_3_out, A);
  and and_1 (and_1_out, not_1_out, B);
  and and_2 (and_2_out, A, not_2_out);
  and and_3 (S1, not_3_out, B);
  or or_1 (S0, and_1_out, and_2_out);
endmodule

module full_subtractor (
  input  A,
  input  B,
  input  C,
  output S0,
  output S1
);

  wire haf_subtractor_1_s0, haf_subtractor_1_s1, haf_subtractor_2_s1;

  haf_subtractor haf_subtractor_1 (.A(A), .B(B), .S0(haf_subtractor_1_s0), .S1(haf_subtractor_1_s1));
  haf_subtractor haf_subtractor_2 (.A(haf_subtractor_1_s0), .B(C), .S0(S0), .S1(haf_subtractor_2_s1));
  or or_1 (S1, haf_subtractor_2_s1, haf_subtractor_1_s1);
endmodule

module Somador_4bits (
  input  a3,
  input  a2,
  input  a1,
  input  a0,
  input  b3,
  input  b2,
  input  b1,
  input  b0,
  output aux_overflow,
  output carry,
  output [3:0] s
);

  wire full_adder_1_s1, full_adder_2_s1, full_adder_3_s1;

  full_adder full_adder_1 (.A(a0), .B(b0), .C(1'b0), .S0(s[0]), .S1(full_adder_1_s1));
  full_adder full_adder_2 (.A(a1), .B(b1), .C(full_adder_1_s1), .S0(s[1]), .S1(full_adder_2_s1));
  full_adder full_adder_3 (.A(a2), .B(b2), .C(full_adder_2_s1), .S0(s[2]), .S1(full_adder_3_s1));
  full_adder full_adder_4 (.A(a3), .B(b3), .C(full_adder_3_s1), .S0(s[3]), .S1(carry));
  not not_1 (aux_overflow, full_adder_3_s1);

  // Notes on the sheet:
  //   A + B
  //   full-adder
  //   full-adder
  //   full-adder
endmodule

module Subtrator_4bits (
  input  a3,
  input  a2,
  input  a1,
  input  a0,
  input  b3,
  input  b2,
  input  b1,
  input  b0,
  output [3:0] s,
  output comparador
);

  wire full_subtractor_1_s1, full_subtractor_2_s1, full_subtractor_3_s1;

  full_subtractor full_subtractor_1 (.A(a0), .B(b0), .C(1'b0), .S0(s[0]), .S1(full_subtractor_1_s1));
  full_subtractor full_subtractor_2 (.A(a1), .B(b1), .C(full_subtractor_1_s1), .S0(s[1]), .S1(full_subtractor_2_s1));
  full_subtractor full_subtractor_3 (.A(a2), .B(b2), .C(full_subtractor_2_s1), .S0(s[2]), .S1(full_subtractor_3_s1));
  full_subtractor full_subtractor_4 (.A(a3), .B(b3), .C(full_subtractor_3_s1), .S0(s[3]), .S1(comparador));

  // Notes on the sheet:
  //   A - B
  //   full-subtractor
  //   full-subtractor
  //   1: a é maior
  //   0: a é menor
endmodule

module Comparador_logico_4bits (
  input  a3,
  input  a2,
  input  a1,
  input  a0,
  input  b3,
  input  b2,
  input  b1,
  input  b0,
  output s
);

  wire xor_1_out, xor_2_out, xor_3_out, xor_4_out;

  xor xor_1 (xor_1_out, b0, a0);
  xor xor_2 (xor_2_out, b1, a1);
  xor xor_3 (xor_3_out, b2, a2);
  xor xor_4 (xor_4_out, b3, a3);
  or or_1 (s, xor_1_out, xor_2_out, xor_3_out, xor_4_out);

  // Notes on the sheet:
  //   0: é igual
  //   1: é diferente
endmodule

module complemento_de_um (
  input  a3,
  input  a2,
  input  a1,
  input  a0,
  output [3:0] s
);

  not not_1 (s[0], a0);
  not not_2 (s[1], a1);
  not not_3 (s[2], a2);
  not not_4 (s[3], a3);
endmodule

module complemento_de_dois (
  input  a3,
  input  a2,
  input  a1,
  input  a0,
  output [3:0] complemento_de_2
);

  wire [3:0] complemento_de_um_1_s;

  complemento_de_um complemento_de_um_1 (.a3(a3), .a2(a2), .a1(a1), .a0(a0), .s(complemento_de_um_1_s));
  Somador_4bits somador_4bits_1 (
    .a3(complemento_de_um_1_s[3]), .a2(complemento_de_um_1_s[2]), .a1(complemento_de_um_1_s[1]),
    .a0(complemento_de_um_1_s[0]), .b3(1'b0), .b2(1'b0), .b1(1'b0), .b0(1'b1), .s(complemento_de_2));  // open: aux_overflow, carry
endmodule

module incremento_de_um (
  input  a3,
  input  a2,
  input  a1,
  input  a0,
  output [3:0] incremento_de_1
);

  Somador_4bits somador_4bits_1 (
    .a3(a3), .a2(a2), .a1(a1), .a0(a0), .b3(1'b0), .b2(1'b0), .b1(1'b0), .b0(1'b1), .s(incremento_de_1));  // open: aux_overflow, carry
endmodule

module decremento_de_1 (
  input  a3,
  input  a2,
  input  a1,
  input  a0,
  output [3:0] decremento_de_1
);

  Subtrator_4bits subtrator_4bits_1 (
    .a3(a3), .a2(a2), .a1(a1), .a0(a0), .b3(1'b0), .b2(1'b0), .b1(1'b0), .b0(1'b1), .s(decremento_de_1));  // open: comparador
endmodule

module produto_por_2 (
  input  a3,
  input  a2,
  input  a1,
  input  a0,
  output [3:0] produto_por_2,
  output errado
);

  xor xor_1 (errado, a3, a2);

  assign produto_por_2 = {a2, a1, a0, 1'b0};
endmodule

module ALU_4bits (
  input  a3,
  input  a2,
  input  a1,
  input  a0,
  input  b3,
  input  b2,
  input  b1,
  input  b0,
  output ZERO_NA_SOMA,
  output [3:0] SOMA,
  output OVERFLOW,
  output CARRY,
  output A_OU_B_ZERO,
  output DIFERENTE,
  output [3:0] complemento_de_1_de_A,
  output [3:0] complemento_de_1_de_B,
  output ZERO_NA_SUBTRACAO,
  output [3:0] A___B,
  output A___B_2,
  output [3:0] complemento_de_2_de_A,
  output [3:0] complemento_de_2_de_B,
  output [3:0] incremento_de_1_de_A,
  output [3:0] incremento_de_1_de_B,
  output [3:0] decremento_de_1_de_A,
  output [3:0] decremento_de_1_de_B,
  output produto_de_A_errado,
  output [3:0] produto_por_2_de_A,
  output produto_de_B_errado,
  output [3:0] produto_por_2_de_B
);

  wire somador_4bits_1_aux_overflow;

  complemento_de_dois complemento_de_dois_1 (
    .a3(a3), .a2(a2), .a1(a1), .a0(a0), .complemento_de_2(complemento_de_2_de_A));
  complemento_de_dois complemento_de_dois_2 (
    .a3(b3), .a2(b2), .a1(b1), .a0(b0), .complemento_de_2(complemento_de_2_de_B));
  incremento_de_um incremento_de_um_1 (.a3(a3), .a2(a2), .a1(a1), .a0(a0), .incremento_de_1(incremento_de_1_de_A));
  incremento_de_um incremento_de_um_2 (.a3(b3), .a2(b2), .a1(b1), .a0(b0), .incremento_de_1(incremento_de_1_de_B));
  decremento_de_1 decremento_de_1_1 (.a3(a3), .a2(a2), .a1(a1), .a0(a0), .decremento_de_1(decremento_de_1_de_A));
  decremento_de_1 decremento_de_1_2 (.a3(b3), .a2(b2), .a1(b1), .a0(b0), .decremento_de_1(decremento_de_1_de_B));
  produto_por_2 produto_por_2_1 (
    .a3(a3), .a2(a2), .a1(a1), .a0(a0), .errado(produto_de_A_errado), .produto_por_2(produto_por_2_de_A));
  produto_por_2 produto_por_2_2 (
    .a3(b3), .a2(b2), .a1(b1), .a0(b0), .errado(produto_de_B_errado), .produto_por_2(produto_por_2_de_B));
  Somador_4bits somador_4bits_1 (
    .a3(a3), .a2(a2), .a1(a1), .a0(a0), .b3(b3), .b2(b2), .b1(b1), .b0(b0), .s(SOMA),
    .aux_overflow(somador_4bits_1_aux_overflow), .carry(CARRY));
  Comparador_logico_4bits comparador_logico_4bits_1 (
    .a3(a3), .a2(a2), .a1(a1), .a0(a0), .b3(b3), .b2(b2), .b1(b1), .b0(b0), .s(DIFERENTE));
  complemento_de_um complemento_de_um_1 (.a3(a3), .a2(a2), .a1(a1), .a0(a0), .s(complemento_de_1_de_A));
  complemento_de_um complemento_de_um_2 (.a3(b3), .a2(b2), .a1(b1), .a0(b0), .s(complemento_de_1_de_B));
  Subtrator_4bits subtrator_4bits_1 (
    .a3(a3), .a2(a2), .a1(a1), .a0(a0), .b3(b3), .b2(b2), .b1(b1), .b0(b0), .s(A___B), .comparador(A___B_2));
  nor nor_1 (A_OU_B_ZERO, a3, a2, a1, a0, b3, b2, b1, b0);
  nor nor_2 (ZERO_NA_SOMA, SOMA[0], SOMA[1], SOMA[2], SOMA[3]);
  nor nor_3 (ZERO_NA_SUBTRACAO, A___B[0], A___B[1], A___B[2], A___B[3]);
  and and_1 (OVERFLOW, CARRY, somador_4bits_1_aux_overflow);

  // Notes on the sheet:
  //   somador_4bits - indicador de overflow e indicador de carry
  //   comparador lógico
endmodule
