// Logisim project Guia07.circ as structural Verilog: 7 circuits, main circuit meia soma
module meia_soma (
  input  in_1,
  input  in_2,
  output out_3,
  output out_4
);

  xor xor_1 (out_3, in_1, in_2);
  and and_1 (out_4, in_2, in_1);
endmodule

module Soma_completa (
  input  in_1,
  input  in_2,
  input  in_3,
  output out_4,
  output out_5
);

  wire meia_soma_1_out_3, meia_soma_1_out_4, meia_soma_2_out_4;

  meia_soma meia_soma_1 (.in_1(in_1), .in_2(in_2), .out_3(meia_soma_1_out_3), .out_4(meia_soma_1_out_4));
  meia_soma meia_soma_2 (.in_1(meia_soma_1_out_3), .in_2(in_3), .out_3(out_4), .out_4(meia_soma_2_out_4));
  or or_1 (out_5, meia_soma_2_out_4, meia_soma_1_out_4);
endmodule

module Soma_4_bits (
  input  [3:0] in_1,
  input  [3:0] in_2,
  output [3:0] out_3,
  output out_4
);

  wire meia_soma_1_out_4, soma_completa_1_out_5, soma_completa_2_out_5;

  meia_soma meia_soma_1 (.in_1(in_1[0]), .in_2(in_2[0]), .out_3(out_3[0]), .out_4(meia_soma_1_out_4));
  Soma_completa soma_completa_1 (
    .in_1(meia_soma_1_out_4), .in_2(in_1[1]), .in_3(in_2[1]), .out_4(out_3[1]), .out_5(soma_completa_1_out_5));
  Soma_completa soma_completa_2 (
    .in_1(soma_completa_1_out_5), .in_2(in_1[2]), .in_3(in_2[2]), .out_4(out_3[2]),
    .out_5(soma_completa_2_out_5));
  Soma_completa soma_completa_3 (
    .in_1(soma_completa_2_out_5), .in_2(in_1[3]), .in_3(in_2[3]), .out_4(out_3[3]), .out_5(out_4));
endmodule

module Complemento_de_2 (
  input  [3:0] in_1,
  output [3:0] out_2
);

  wire [3:0] not_1_out;

  assign not_1_out = ~in_1;  // NOT_Gate not_1, 4 bits wide
  Soma_4_bits soma_4_bits_1 (.in_1(not_1_out), .in_2(4'b0001), .out_3(out_2));  // open: out_4
endmodule

module Complemento_de_1 (
  input  [3:0] in_1,
  output [3:0] out_2
);

  assign out_2 = ~in_1;  // NOT_Gate not_1, 4 bits wide
endmodule

module Incremento_1 (
  input  [3:0] in_1,
  output [3:0] out_2,
  output out_3
);

  Soma_4_bits soma_4_bits_1 (.in_1(in_1), .in_2(4'b0001), .out_3(out_2), .out_4(out_3));
endmodule

module ALU (
  input  [3:0] in_1,
  input  [3:0] in_2,
  input  [2:0] in_3,
  output [3:0] out_4
);

  wire [3:0] complemento_de_1_1_out_2, complemento_de_1_2_out_2, complemento_de_2_1_out_2,
       complemento_de_2_2_out_2, incremento_1_1_out_2, incremento_1_2_out_2;

  Complemento_de_2 complemento_de_2_1 (.in_1(in_1), .out_2(complemento_de_2_1_out_2));
  Complemento_de_2 complemento_de_2_2 (.in_1(in_2), .out_2(complemento_de_2_2_out_2));
  Complemento_de_1 complemento_de_1_1 (.in_1(in_1), .out_2(complemento_de_1_1_out_2));
  Complemento_de_1 complemento_de_1_2 (.in_1(in_2), .out_2(complemento_de_1_2_out_2));
  Incremento_1 incremento_1_1 (.in_1(in_1), .out_2(incremento_1_1_out_2));  // open: out_3
  Incremento_1 incremento_1_2 (.in_1(in_2), .out_2(incremento_1_2_out_2));  // open: out_3
  Multiplexer #(.select(3), .width(4)) multiplexer_1 (
    .in0(complemento_de_2_1_out_2), .in1(complemento_de_2_2_out_2), .in2(complemento_de_1_1_out_2),
    .in3(complemento_de_1_2_out_2), .in6(incremento_1_1_out_2), .in7(incremento_1_2_out_2), .out(out_4),
    .sel(in_3));  // open: in4, in5
endmodule
