// Logisim project exercicio04.circ as structural Verilog: 15 circuits, main circuit main
module main (
  input  [3:0] a,
  input  [3:0] b,
  output [3:0] Complemento_1,
  output [3:0] Complemento_1_2,
  output [3:0] Complemento_2,
  output Overflow,
  output [3:0] Complemento_2_2,
  output Overflow_2,
  output [3:0] Incremento_1,
  output Overflow_3,
  output [3:0] Incremento_1_2,
  output Overflow_4
);

  complemento1 complemento1_1 (.in_1(a), .complemento(Complemento_1));
  complemento1 complemento1_2 (.in_1(b), .complemento(Complemento_1_2));
  complemento2 complemento2_1 (.a(a), .Complemento2(Complemento_2), .Overflow(Overflow));
  complemento2 complemento2_2 (.a(b), .Complemento2(Complemento_2_2), .Overflow(Overflow_2));
  incremento1 incremento1_1 (.a(a), .Resultado(Incremento_1), .Overflow(Overflow_3));
  incremento1 incremento1_2 (.a(b), .Resultado(Incremento_1_2), .Overflow(Overflow_4));

  // Notes on the sheet:
  //   Guia_07 - Exercicio03
  //   Inclusão em uma ALU de 4 bits decremento de 1
  //   Autor: Tiago Menegaz de Melo Garcia
  //   Matrícula: 405844
endmodule

module equals (
  input  in_1,
  input  in_2,
  input  in_3,
  input  in_4,
  input  in_5,
  input  in_6,
  input  in_7,
  input  in_8,
  output out_9
);

  wire xnor_1_out, xnor_2_out, xnor_3_out, xnor_4_out;

  xnor xnor_1 (xnor_1_out, in_1, in_5);
  xnor xnor_2 (xnor_2_out, in_2, in_6);
  xnor xnor_3 (xnor_3_out, in_3, in_7);
  xnor xnor_4 (xnor_4_out, in_4, in_8);
  and and_1 (out_9, xnor_1_out, xnor_2_out, xnor_3_out, xnor_4_out);
endmodule

module full_adder (
  input  vem_um,
  input  a,
  input  b,
  output Resto,
  output Vai_um
);

  wire and_1_out, and_2_out, xor_1_out;

  xor xor_1 (xor_1_out, a, b);
  and and_1 (and_1_out, b, a);
  xor xor_2 (Resto, vem_um, xor_1_out);
  and and_2 (and_2_out, vem_um, xor_1_out);
  or or_1 (Vai_um, and_2_out, and_1_out);
endmodule

module half_adder (
  input  a,
  input  b,
  output Resto,
  output Vai_um
);

  xor xor_1 (Resto, a, b);
  and and_1 (Vai_um, b, a);
endmodule

module complete_adder (
  input  a0,
  input  a1,
  input  a2,
  input  b0,
  input  b1,
  input  b2,
  output [2:0] Resultado,
  output Overflow
);

  wire full_adder_1_vai_um, half_adder_1_vai_um;

  half_adder half_adder_1 (.a(a0), .b(b0), .Resto(Resultado[0]), .Vai_um(half_adder_1_vai_um));
  full_adder full_adder_1 (
    .vem_um(half_adder_1_vai_um), .a(a1), .b(b1), .Resto(Resultado[1]), .Vai_um(full_adder_1_vai_um));
  full_adder full_adder_2 (.vem_um(full_adder_1_vai_um), .a(a2), .b(b2), .Resto(Resultado[2]), .Vai_um(Overflow));
endmodule

module half_subtractor (
  input  a,
  input  b,
  output Resto,
  output Vem_um
);

  wire buffer_1_out;

  buf buffer_1 (buffer_1_out, a);
  xor xor_1 (Resto, a, b);
  and and_1 (Vem_um, b, buffer_1_out);
endmodule

module full_subtractor (
  input  Vem_um,
  input  a,
  input  b,
  output Resto,
  output Vem_um_2
);

  wire and_1_out, and_2_out, buffer_1_out, buffer_2_out, xor_1_out;

  xor xor_1 (xor_1_out, b, a);
  and and_1 (and_1_out, b, buffer_1_out);
  buf buffer_1 (buffer_1_out, a);
  xor xor_2 (Resto, Vem_um, xor_1_out);
  and and_2 (and_2_out, Vem_um, buffer_2_out);
  buf buffer_2 (buffer_2_out, xor_1_out);
  // NOT_Gate not_1 is placed but not wired
  or or_1 (Vem_um_2, and_2_out, and_1_out);
endmodule

module complete_subtractor (
  input  a0,
  input  a1,
  input  a2,
  input  b0,
  input  b1,
  input  b2,
  output [2:0] Resultado,
  output Vem_um
);

  wire full_subtractor_1_vem_um_2, half_subtractor_1_vem_um;

  half_subtractor half_subtractor_1 (.a(b0), .b(a0), .Resto(Resultado[0]), .Vem_um(half_subtractor_1_vem_um));
  full_subtractor full_subtractor_1 (
    .Vem_um(half_subtractor_1_vem_um), .a(b1), .b(a1), .Resto(Resultado[1]),
    .Vem_um_2(full_subtractor_1_vem_um_2));
  full_subtractor full_subtractor_2 (
    .Vem_um(full_subtractor_1_vem_um_2), .a(b2), .b(a2), .Resto(Resultado[2]), .Vem_um_2(Vem_um));
endmodule

module comparador (
  input  a0,
  input  a1,
  input  a2,
  input  Sinal,
  input  b0,
  input  b1,
  input  b2,
  input  Sinal_2
);

  // NOT_Gate not_1 has open pins: in=a0, out=open
  // NOT_Gate not_2 has open pins: in=a1, out=open
  // NOT_Gate not_3 has open pins: in=a2, out=open
  // NOT_Gate not_4 has open pins: in=Sinal, out=open
  // NOT_Gate not_5 has open pins: in=b0, out=open
  // NOT_Gate not_6 has open pins: in=b1, out=open
  // NOT_Gate not_7 has open pins: in=b2, out=open
  // NOT_Gate not_8 has open pins: in=Sinal_2, out=open
endmodule

module complemento1 (
  input  [3:0] in_1,
  output [3:0] complemento
);

  assign complemento = ~in_1;  // NOT_Gate not_1, 4 bits wide
endmodule

module \and  (
  input  [2:0] in_1,
  output out_2
);

  and and_1 (out_2, in_1[0], in_1[1], in_1[2]);
endmodule

module \or  (
  input  [2:0] in_1,
  output out_2
);

  or or_1 (out_2, in_1[0], in_1[1], in_1[2]);
endmodule

module complemento2 (
  input  [3:0] a,
  output [3:0] Complemento2,
  output Overflow
);

  wire full_adder_1_vai_um, full_adder_2_vai_um, half_adder_1_vai_um;

  half_adder half_adder_1 (.a(a[0]), .b(1'b1), .Resto(Complemento2[0]), .Vai_um(half_adder_1_vai_um));
  full_adder full_adder_1 (
    .vem_um(half_adder_1_vai_um), .a(a[2]), .b(1'b0), .Resto(Complemento2[1]), .Vai_um(full_adder_1_vai_um));
  full_adder full_adder_2 (
    .vem_um(full_adder_1_vai_um), .a(a[2]), .b(1'b0), .Resto(Complemento2[2]), .Vai_um(full_adder_2_vai_um));
  full_adder full_adder_3 (
    .vem_um(full_adder_2_vai_um), .a(a[3]), .b(1'b0), .Resto(Complemento2[3]), .Vai_um(Overflow));

  assign a[1] = a[2];
endmodule

module incremento1 (
  input  [3:0] a,
  output [3:0] Resultado,
  output Overflow
);

  wire full_adder_1_vai_um, full_adder_2_vai_um, half_adder_1_vai_um;

  half_adder half_adder_1 (.a(a[0]), .b(1'b1), .Resto(Resultado[0]), .Vai_um(half_adder_1_vai_um));
  full_adder full_adder_1 (
    .vem_um(half_adder_1_vai_um), .a(a[1]), .b(1'b0), .Resto(Resultado[1]), .Vai_um(full_adder_1_vai_um));
  full_adder full_adder_2 (
    .vem_um(full_adder_1_vai_um), .a(a[2]), .b(1'b0), .Resto(Resultado[2]), .Vai_um(full_adder_2_vai_um));
  full_adder full_adder_3 (.vem_um(full_adder_2_vai_um), .a(a[3]), .b(1'b0), .Resto(Resultado[3]), .Vai_um(Overflow));
endmodule

module decremento1 (
  input  [3:0] a,
  output [3:0] Resultado,
  output Overflow
);

  wire full_subtractor_1_vem_um_2, full_subtractor_2_vem_um_2, half_subtractor_1_vem_um;

  half_subtractor half_subtractor_1 (.a(a[0]), .b(1'b1), .Resto(Resultado[0]), .Vem_um(half_subtractor_1_vem_um));
  full_subtractor full_subtractor_1 (
    .Vem_um(half_subtractor_1_vem_um), .a(a[1]), .b(1'b0), .Resto(Resultado[1]),
    .Vem_um_2(full_subtractor_1_vem_um_2));
  full_subtractor full_subtractor_2 (
    .Vem_um(full_subtractor_1_vem_um_2), .a(a[2]), .b(1'b0), .Resto(Resultado[2]),
    .Vem_um_2(full_subtractor_2_vem_um_2));
  full_subtractor full_subtractor_3 (
    .Vem_um(full_subtractor_2_vem_um_2), .a(a[3]), .b(1'b0), .Resto(Resultado[3]), .Vem_um_2(Overflow));
endmodule
