// Logisim project guia6.circ as structural Verilog: 15 circuits, main circuit meiasoma
module meiasoma (
  input  a,
  input  b,
  output so,
  output s1
);

  xor xor_1 (so, a, b);
  and and_1 (s1, b, a);
endmodule

module somacompleta (
  input  c,
  input  a,
  input  b,
  output s0,
  output s1
);

  wire meiasoma_1_s1, meiasoma_1_so, meiasoma_2_s1;

  meiasoma meiasoma_1 (.a(a), .b(b), .so(meiasoma_1_so), .s1(meiasoma_1_s1));
  meiasoma meiasoma_2 (.a(c), .b(meiasoma_1_so), .so(s0), .s1(meiasoma_2_s1));
  or or_1 (s1, meiasoma_2_s1, meiasoma_1_s1);
endmodule

module soma_sub_4_bits (
  input  sinal,
  input  [3:0] a,
  input  [3:0] b,
  output [3:0] saida,
  output carry_out
);

  wire somacompleta_1_s1, somacompleta_2_s1, somacompleta_3_s1, xor_1_out, xor_2_out, xor_3_out, xor_4_out;

  xor xor_1 (xor_1_out, sinal, b[0]);
  xor xor_2 (xor_2_out, b[1], sinal);
  xor xor_3 (xor_3_out, b[2], sinal);
  xor xor_4 (xor_4_out, sinal, b[3]);
  somacompleta somacompleta_1 (.c(sinal), .a(a[0]), .b(xor_1_out), .s0(saida[0]), .s1(somacompleta_1_s1));
  somacompleta somacompleta_2 (.c(somacompleta_1_s1), .a(a[1]), .b(xor_2_out), .s0(saida[1]), .s1(somacompleta_2_s1));
  somacompleta somacompleta_3 (.c(somacompleta_2_s1), .a(a[2]), .b(xor_3_out), .s0(saida[2]), .s1(somacompleta_3_s1));
  somacompleta somacompleta_4 (.c(somacompleta_3_s1), .a(a[3]), .b(xor_4_out), .s0(saida[3]), .s1(carry_out));

  // Notes on the sheet:
  //   0 = soma
  //   1 = subtração
endmodule

module comparador (
  input  [3:0] a,
  input  [3:0] b,
  output saida
);

  wire xor_1_out, xor_2_out, xor_3_out, xor_4_out;

  xor xor_1 (xor_1_out, a[0], b[0]);
  xor xor_2 (xor_2_out, a[1], b[1]);
  xor xor_3 (xor_3_out, a[2], b[2]);
  xor xor_4 (xor_4_out, b[3], a[3]);
  or or_1 (saida, xor_1_out, xor_2_out, xor_3_out, xor_4_out);

  // Notes on the sheet:
  //   numeros iguais = 0
  //   numeros diferentes = 1
endmodule

module meiadif (
  input  a,
  input  b,
  output s0,
  output s1
);

  wire not_1_out;

  not not_1 (not_1_out, a);
  xor xor_1 (s0, a, b);
  and and_1 (s1, b, not_1_out);
endmodule

module difcompleta (
  input  c,
  input  a,
  input  b,
  output s0,
  output s1
);

  wire meiadif_1_s0, meiadif_1_s1, meiadif_2_s1;

  meiadif meiadif_1 (.a(a), .b(b), .s0(meiadif_1_s0), .s1(meiadif_1_s1));
  meiadif meiadif_2 (.a(meiadif_1_s0), .b(c), .s0(s0), .s1(meiadif_2_s1));
  or or_1 (s1, meiadif_2_s1, meiadif_1_s1);
endmodule

module dif4 (
  input  [3:0] a,
  input  [3:0] b,
  output [4:0] saida
);

  wire difcompleta_1_s1, difcompleta_2_s1, meiadif_1_s1;

  meiadif meiadif_1 (.a(a[0]), .b(b[0]), .s0(saida[0]), .s1(meiadif_1_s1));
  difcompleta difcompleta_1 (.c(meiadif_1_s1), .a(a[1]), .b(b[1]), .s0(saida[1]), .s1(difcompleta_1_s1));
  difcompleta difcompleta_2 (.c(difcompleta_1_s1), .a(a[2]), .b(b[2]), .s0(saida[2]), .s1(difcompleta_2_s1));
  difcompleta difcompleta_3 (.c(difcompleta_2_s1), .a(a[3]), .b(b[3]), .s0(saida[3]), .s1(saida[4]));
endmodule

module carry (
  input  sinal,
  input  [3:0] a,
  input  [3:0] b,
  output carry_in,
  output [3:0] saida,
  output carry_out
);

  wire somacompleta_1_s1, somacompleta_2_s1, somacompleta_3_s1, xor_1_out, xor_2_out, xor_3_out, xor_4_out;

  xor xor_1 (xor_1_out, sinal, b[0]);
  xor xor_2 (xor_2_out, b[1], sinal);
  xor xor_3 (xor_3_out, b[2], sinal);
  xor xor_4 (xor_4_out, sinal, b[3]);
  somacompleta somacompleta_1 (.c(sinal), .a(a[0]), .b(xor_1_out), .s0(saida[0]), .s1(somacompleta_1_s1));
  somacompleta somacompleta_2 (.c(somacompleta_1_s1), .a(a[1]), .b(xor_2_out), .s0(saida[1]), .s1(somacompleta_2_s1));
  somacompleta somacompleta_3 (.c(somacompleta_2_s1), .a(a[2]), .b(xor_3_out), .s0(saida[2]), .s1(somacompleta_3_s1));
  somacompleta somacompleta_4 (.c(somacompleta_3_s1), .a(a[3]), .b(xor_4_out), .s0(saida[3]), .s1(carry_out));
  or or_1 (carry_in, somacompleta_1_s1, somacompleta_2_s1, somacompleta_3_s1);

  // Notes on the sheet:
  //   0 = soma
  //   1 = subtração
endmodule

module zero (
  input  sinal,
  input  [3:0] a,
  input  [3:0] b,
  output carry_in,
  output zero,
  output [3:0] saida,
  output carry_out
);

  wire somacompleta_1_s1, somacompleta_2_s1, somacompleta_3_s1, xor_1_out, xor_2_out, xor_3_out, xor_4_out;

  xor xor_1 (xor_1_out, sinal, b[0]);
  xor xor_2 (xor_2_out, b[1], sinal);
  xor xor_3 (xor_3_out, b[2], sinal);
  xor xor_4 (xor_4_out, sinal, b[3]);
  somacompleta somacompleta_1 (.c(sinal), .a(a[0]), .b(xor_1_out), .s0(saida[0]), .s1(somacompleta_1_s1));
  somacompleta somacompleta_2 (.c(somacompleta_1_s1), .a(a[1]), .b(xor_2_out), .s0(saida[1]), .s1(somacompleta_2_s1));
  somacompleta somacompleta_3 (.c(somacompleta_2_s1), .a(a[2]), .b(xor_3_out), .s0(saida[3]), .s1(somacompleta_3_s1));
  somacompleta somacompleta_4 (.c(somacompleta_3_s1), .a(a[3]), .b(xor_4_out), .s0(saida[3]), .s1(carry_out));
  or or_1 (carry_in, somacompleta_1_s1, somacompleta_2_s1, somacompleta_3_s1);
  nor nor_1 (zero, saida[0], saida[1], saida[3], saida[3]);

  assign saida[2] = saida[3];

  // Notes on the sheet:
  //   0 = soma
  //   1 = subtração
endmodule

module overflow (
  input  sinal,
  input  [3:0] a,
  input  [3:0] b,
  output carry_in,
  output zero,
  output [3:0] saida,
  output carry_out,
  output overflow
);

  wire somacompleta_1_s1, somacompleta_2_s1, somacompleta_3_s1, xor_1_out, xor_2_out, xor_3_out, xor_4_out;

  xor xor_1 (xor_1_out, sinal, b[0]);
  xor xor_2 (xor_2_out, b[1], sinal);
  xor xor_3 (xor_3_out, b[2], sinal);
  xor xor_4 (xor_4_out, sinal, b[3]);
  somacompleta somacompleta_1 (.c(sinal), .a(a[0]), .b(xor_1_out), .s0(saida[0]), .s1(somacompleta_1_s1));
  somacompleta somacompleta_2 (.c(somacompleta_1_s1), .a(a[1]), .b(xor_2_out), .s0(saida[1]), .s1(somacompleta_2_s1));
  somacompleta somacompleta_3 (.c(somacompleta_2_s1), .a(a[2]), .b(xor_3_out), .s0(saida[2]), .s1(somacompleta_3_s1));
  somacompleta somacompleta_4 (.c(somacompleta_3_s1), .a(a[3]), .b(xor_4_out), .s0(saida[3]), .s1(carry_out));
  or or_1 (carry_in, somacompleta_1_s1, somacompleta_2_s1, somacompleta_3_s1);
  xor xor_5 (overflow, carry_out, somacompleta_3_s1);
  nor nor_1 (zero, saida[0], saida[1], saida[2], saida[3]);

  // Notes on the sheet:
  //   0 = soma
  //   1 = subtração
endmodule

module complemento (
  input  a_prime_ou_b_prime,
  input  [3:0] a,
  input  [3:0] b,
  output [3:0] saida
);

  wire and_1_out, and_2_out, and_3_out, and_4_out, and_5_out, and_6_out, and_7_out, and_8_out, not_1_out,
       not_2_out, not_3_out, not_4_out, not_5_out, not_6_out, not_7_out, not_8_out, not_9_out;

  not not_1 (not_1_out, a[0]);
  not not_2 (not_2_out, a[1]);
  not not_3 (not_3_out, a[2]);
  not not_4 (not_4_out, a[3]);
  not not_5 (not_5_out, b[0]);
  not not_6 (not_6_out, b[1]);
  not not_7 (not_7_out, b[2]);
  not not_8 (not_8_out, b[3]);
  not not_9 (not_9_out, a_prime_ou_b_prime);
  and and_1 (and_1_out, a_prime_ou_b_prime, not_5_out);
  and and_2 (and_2_out, a_prime_ou_b_prime, not_6_out);
  and and_3 (and_3_out, a_prime_ou_b_prime, not_7_out);
  and and_4 (and_4_out, a_prime_ou_b_prime, not_8_out);
  and and_5 (and_5_out, not_9_out, not_1_out);
  and and_6 (and_6_out, not_2_out, not_9_out);
  and and_7 (and_7_out, not_3_out, not_9_out);
  and and_8 (and_8_out, not_9_out, not_4_out);
  or or_1 (saida[0], and_5_out, and_1_out);
  or or_2 (saida[1], and_6_out, and_2_out);
  or or_3 (saida[2], and_7_out, and_3_out);
  or or_4 (saida[3], and_4_out, and_8_out);

  // Notes on the sheet:
  //   0
  //   1
endmodule

module incremento (
  input  [3:0] a,
  input  [3:0] b,
  output [3:0] saida,
  output carry_out
);

  wire meiasoma_1_s1, somacompleta_1_s1, somacompleta_2_s1;

  meiasoma meiasoma_1 (.a(a[0]), .b(b[0]), .so(saida[0]), .s1(meiasoma_1_s1));
  somacompleta somacompleta_1 (.c(meiasoma_1_s1), .a(a[1]), .b(b[1]), .s0(saida[1]), .s1(somacompleta_1_s1));
  somacompleta somacompleta_2 (.c(somacompleta_1_s1), .a(a[2]), .b(b[2]), .s0(saida[2]), .s1(somacompleta_2_s1));
  somacompleta somacompleta_3 (.c(somacompleta_2_s1), .a(a[3]), .b(b[3]), .s0(saida[3]), .s1(carry_out));
endmodule

module incremento2 (
  input  [3:0] a,
  output [3:0] saida,
  output carry_out
);

  incremento incremento_1 (.a(a), .b(4'b0001), .saida(saida), .carry_out(carry_out));
endmodule

module complemento_de_2 (
  input  [3:0] in_1,
  output [3:0] out_2,
  output carry_out
);

  wire [3:0] not_1_out;

  assign not_1_out = ~in_1;  // NOT_Gate not_1, 4 bits wide
  incremento incremento_1 (.a(not_1_out), .b(4'b0001), .saida(out_2), .carry_out(carry_out));
endmodule

module main (
  input  sinal,
  input  [3:0] a,
  input  [3:0] b,
  output [3:0] saida,
  output carry_out,
  output _0___igual,
  output carry_in,
  output zero,
  output [3:0] saida_2,
  output crry_out,
  output overflow,
  output [3:0] saida_3,
  output [3:0] saida_4,
  output carry_out_2,
  output [3:0] saida_5,
  output carry_out_3,
  output [3:0] saida_6,
  output carry_out_4
);

  complemento complemento_1 (.a_prime_ou_b_prime(sinal), .a(a), .b(b), .saida(saida_3));
  incremento incremento_1 (.a(a), .b(b), .saida(saida_4), .carry_out(carry_out_2));
  complemento_de_2 complemento_de_2_1 (.in_1(a), .out_2(saida_5), .carry_out(carry_out_3));
  complemento_de_2 complemento_de_2_2 (.in_1(b), .out_2(saida_6), .carry_out(carry_out_4));
  soma_sub_4_bits soma_sub_4_bits_1 (.sinal(sinal), .a(a), .b(b), .saida(saida), .carry_out(carry_out));
  comparador comparador_1 (.a(a), .b(b), .saida(_0___igual));
  overflow overflow_1 (
    .sinal(sinal), .a(a), .b(b), .carry_in(carry_in), .zero(zero), .saida(saida_2), .carry_out(crry_out),
    .overflow(overflow));

  // Notes on the sheet:
  //   obs : Não sei fazer com mux.
  //   complemento de 2 de A
  //   complemento de 2 de B
  //   1 = diferentes
endmodule
