// Logisim project Guia07.circ as structural Verilog: 9 circuits, main circuit main
module main (
  input  [3:0] a,
  output [3:0] C1,
  output [3:0] C2,
  output [3:0] inc1,
  output [3:0] dec1,
  output [4:0] x2
);

  C1 c1_1 (.a(a), .s(C1));
  C2 c2_1 (.a(a), .s(C2));
  Inc1 inc1_1 (.a(a), .s(inc1));
  Dec1 dec1_1 (.a(a), .s(dec1));
  x2 x2_1 (.a(a), .s(x2));

  // Notes on the sheet:
  //   ALU Guia07
endmodule

module MeiaSoma (
  input  a,
  input  b,
  output s,
  output c
);

  and and_1 (c, a, b);
  xor xor_1 (s, a, b);
endmodule

module SomaCompleta (
  input  cin,
  input  a,
  input  b,
  output s,
  output c
);

  wire meiasoma_1_c, meiasoma_1_s, meiasoma_2_c;

  MeiaSoma meiasoma_1 (.a(cin), .b(a), .s(meiasoma_1_s), .c(meiasoma_1_c));
  MeiaSoma meiasoma_2 (.a(meiasoma_1_s), .b(b), .s(s), .c(meiasoma_2_c));
  or or_1 (c, meiasoma_2_c, meiasoma_1_c);
endmodule

module Soma4B (
  input  [3:0] a,
  input  [3:0] b,
  output [3:0] S,
  output cout,
  output overflow
);

  wire not_1_out, somacompleta_1_c, somacompleta_2_c, somacompleta_3_c, somacompleta_4_c;

  SomaCompleta somacompleta_1 (.cin(1'b0), .a(a[0]), .b(b[0]), .s(S[0]), .c(somacompleta_1_c));
  SomaCompleta somacompleta_2 (.cin(somacompleta_1_c), .a(a[1]), .b(b[1]), .s(S[1]), .c(somacompleta_2_c));
  SomaCompleta somacompleta_3 (.cin(somacompleta_2_c), .a(a[2]), .b(b[2]), .s(S[2]), .c(somacompleta_3_c));
  SomaCompleta somacompleta_4 (.cin(somacompleta_3_c), .a(a[3]), .b(b[3]), .s(S[3]), .c(somacompleta_4_c));
  not not_1 (not_1_out, somacompleta_4_c);
  xor xor_1 (overflow, somacompleta_4_c, somacompleta_3_c);
  and and_1 (cout, somacompleta_4_c, not_1_out);
endmodule

module C2 (
  input  [3:0] a,
  output [3:0] s
);

  wire [3:0] not_1_out;

  assign not_1_out = ~a;  // NOT_Gate not_1, 4 bits wide
  Soma4B soma4b_1 (.a(4'b0001), .b(not_1_out), .S(s));  // open: cout, overflow

  // Notes on the sheet:
  //   C2 = C1 + 1
endmodule

module C1 (
  input  [3:0] a,
  output [3:0] s
);

  assign s = ~a;  // NOT_Gate not_1, 4 bits wide

  // Notes on the sheet:
  //   C1 = Inverso.
endmodule

module Inc1 (
  input  [3:0] a,
  output [3:0] s
);

  Soma4B soma4b_1 (.a(4'b0001), .b(a), .S(s));  // open: cout, overflow

  // Notes on the sheet:
  //   +1
endmodule

module Dec1 (
  input  [3:0] a,
  output [3:0] s
);

  wire [3:0] c2_1_s;

  C2 c2_1 (.a(4'b0001), .s(c2_1_s));
  Soma4B soma4b_1 (.a(c2_1_s), .b(a), .S(s));  // open: cout, overflow

  // Notes on the sheet:
  //   = 1111
endmodule

module x2 (
  input  [3:0] a,
  output [4:0] s
);


  assign s = {a, 1'b0};

  // Notes on the sheet:
  //   Deslocar bits pra esquerda
endmodule
