// Logisim project Exercicio_guia7.circ as structural Verilog
module meia_soma (
  input  a,
  input  b,
  output s1,
  output s0
);

  xor xor_1 (s1, a, b);
  and and_1 (s0, a, a, b);

  // Notes on the sheet:
  //   MEIA-SOMA
endmodule

module soma_completa (
  input  carry_in,
  input  a,
  input  b,
  output s1,
  output s0
);

  wire meia_soma_1_s0, meia_soma_1_s1, meia_soma_2_s0;

  meia_soma meia_soma_1 (.a(a), .b(b), .s1(meia_soma_1_s1), .s0(meia_soma_1_s0));
  meia_soma meia_soma_2 (.a(carry_in), .b(meia_soma_1_s1), .s1(s1), .s0(meia_soma_2_s0));
  or or_1 (s0, meia_soma_2_s0, meia_soma_1_s0);

  // Notes on the sheet:
  //   SOMA-COMPLETA
endmodule

module soma4bits (
  input  [3:0] a,
  input  [3:0] b,
  output [3:0] resultado
);

  wire meia_soma_1_s0, soma_completa_1_s0, soma_completa_2_s0;

  meia_soma meia_soma_1 (.a(a[0]), .b(b[0]), .s1(resultado[0]), .s0(meia_soma_1_s0));
  soma_completa soma_completa_1 (
    .carry_in(meia_soma_1_s0), .a(a[1]), .b(b[1]), .s1(resultado[1]), .s0(soma_completa_1_s0));
  soma_completa soma_completa_2 (
    .carry_in(soma_completa_1_s0), .a(a[2]), .b(b[2]), .s1(resultado[2]), .s0(soma_completa_2_s0));
  soma_completa soma_completa_3 (.carry_in(soma_completa_2_s0), .a(a[3]), .b(b[3]), .s1(resultado[3]));  // open: s0

  // Notes on the sheet:
  //   SOMA_4BITS
endmodule

module comparar (
  input  [3:0] a,
  input  [3:0] b,
  output _0_diferentes,
  output [3:0] resultado
);

  wire [3:0] xnor_1_out;

  assign xnor_1_out = ~(a ^ b);  // XNOR_Gate xnor_1, 4 bits wide
  soma4bits soma4bits_1 (.a(a), .b(b), .resultado(resultado));
  and and_1 (_0_diferentes, xnor_1_out[0], xnor_1_out[1], xnor_1_out[2], xnor_1_out[3]);

  // Notes on the sheet:
  //   SOMA-COMPARAÇÃO
  //   1-iguais
endmodule

module \meia_diferença  (
  input  a,
  input  b,
  output s0,
  output s1
);

  wire not_1_out;

  not not_1 (not_1_out, a);
  xor xor_1 (s0, a, b);
  and and_1 (s1, b, not_1_out);

  // Notes on the sheet:
  //   MEIA-DIFERENÇA
endmodule

module \diferença_completa  (
  input  carry,
  input  a,
  input  b,
  output s0,
  output s1
);

  wire and_1_out, and_2_out, not_1_out, not_2_out, xor_1_out;

  xor xor_1 (xor_1_out, a, b);
  not not_1 (not_1_out, a);
  and and_1 (and_1_out, not_1_out, b);
  not not_2 (not_2_out, xor_1_out);
  xor xor_2 (s0, carry, xor_1_out);
  and and_2 (and_2_out, carry, not_2_out);
  or or_1 (s1, and_2_out, and_1_out);

  // Notes on the sheet:
  //   DIFERENÇA-COMPLETA
endmodule

module \diferença4bits  (
  input  [3:0] a,
  input  [3:0] b,
  output [3:0] Resultado,
  output out_4
);

  wire \diferença_completa_1_s1 , \diferença_completa_2_s1 , \meia_diferença_1_s1 ;

  \meia_diferença  \meia_diferença_1  (.a(a[0]), .b(b[0]), .s0(Resultado[0]), .s1(\meia_diferença_1_s1 ));
  \diferença_completa  \diferença_completa_1  (
    .carry(\meia_diferença_1_s1 ), .a(a[1]), .b(b[1]), .s0(Resultado[1]), .s1(\diferença_completa_1_s1 ));
  \diferença_completa  \diferença_completa_2  (
    .carry(\diferença_completa_1_s1 ), .a(a[2]), .b(b[2]), .s0(Resultado[2]), .s1(\diferença_completa_2_s1 ));
  \diferença_completa  \diferença_completa_3  (
    .carry(\diferença_completa_2_s1 ), .a(a[3]), .b(b[3]), .s0(out_4));  // open: s1

  assign Resultado[3] = out_4;

  // Notes on the sheet:
  //   DIFERENÇA-4BITS
endmodule

module complemento_de_um (
  input  [3:0] in_1,
  output [3:0] out_2
);

  assign out_2 = ~in_1;  // NOT_Gate not_1, 4 bits wide

  // Notes on the sheet:
  //   COMPLEMENTO DE 1
endmodule

module incrementar_1 (
  input  [3:0] in_1,
  output [3:0] out_2
);

  soma4bits soma4bits_1 (.a(4'b0001), .b(in_1), .resultado(out_2));

  // Notes on the sheet:
  //   INCREMENTAR 1
endmodule

module complemento__de_dois (
  input  [3:0] in_1,
  output [3:0] out_2
);

  wire [3:0] not_1_out;

  assign not_1_out = ~in_1;  // NOT_Gate not_1, 4 bits wide
  incrementar_1 incrementar_1_1 (.in_1(not_1_out), .out_2(out_2));

  // Notes on the sheet:
  //   COMPLEMENTO DE 2
endmodule

module decrementar_1 (
  input  [3:0] in_1,
  output [3:0] out_2
);

  \diferença4bits  \diferença4bits_1  (.a(in_1), .b(4'b0001), .Resultado(out_2));  // open: out_4

  // Notes on the sheet:
  //   DECREMENAR 1
endmodule

module produto_2 (
  input  [3:0] in_1,
  output [3:0] out_2
);

  soma4bits soma4bits_1 (.a(in_1), .b(in_1), .resultado(out_2));

  // Notes on the sheet:
  //   PRODUTO POR 2
endmodule

module ALU (
  input  [3:0] a,
  input  [3:0] b,
  output [3:0] soma,
  output [3:0] \subtração ,
  output [3:0] incremento_de_1,
  output [3:0] complemento_de_1,
  output [3:0] complemento_de_2,
  output [3:0] produto_por_2
);

  soma4bits soma4bits_1 (.a(a), .b(b), .resultado(soma));
  \diferença4bits  \diferença4bits_1  (.a(a), .b(b), .Resultado(\subtração ));  // open: out_4
  incrementar_1 incrementar_1_1 (.in_1(b), .out_2(incremento_de_1));
  complemento_de_um complemento_de_um_1 (.in_1(b), .out_2(complemento_de_1));
  complemento__de_dois complemento__de_dois_1 (.in_1(b), .out_2(complemento_de_2));
  produto_2 produto_2_1 (.in_1(b), .out_2(produto_por_2));

  // Notes on the sheet:
  //   UNIDADE LÓGICA ARITMÉTICA
endmodule
