// Logisim project ALU2.circ as structural Verilog: 13 circuits, main circuit main
module main (
  input  [3:0] a,
  input  [3:0] b,
  output [5:0] out_3,
  output _0___igual,
  output [4:0] out_5,
  output out_6,
  output [3:0] out_7,
  output [3:0] out_8,
  output [4:0] out_9,
  output [4:0] out_10,
  output [4:0] out_11,
  output [4:0] out_12,
  output [4:0] out_13,
  output [4:0] out_14,
  output [3:0] out_15
);

  wire somador_4bits_1_s4, undriven;

  somador_4bits somador_4bits_1 (
    .a(a), .b({a[2:0], b[0]}), .s0(out_3[5]), .s1(out_3[4]), .s2(out_3[3]), .s3(out_3[2]), .c(out_3[1]),
    .s4(somador_4bits_1_s4));
  comparador_logico comparador_logico_1 (.in_1(a), .in_2({a[2:0], b[0]}), .out_3(_0___igual));
  subtrator_4bits subtrator_4bits_1 (.in_1(a), .in_2({a[2:0], b[0]}), .out_3(out_5));
  completamento_de_1 completamento_de_1_1 (.a(a), .b({a[2:0], b[0]}), .s2(out_7), .s1(out_8));
  Complemento_de_2 complemento_de_2_1 (.in_1({a[2:0], b[0]}), .out_2(out_9));
  Complemento_de_2 complemento_de_2_2 (.in_1(a), .out_2(out_10));
  Incremento_de_1 incremento_de_1_1 (.in_1({a[2:0], b[0]}), .out_2(out_11));
  Incremento_de_1 incremento_de_1_2 (.in_1(a), .out_2(out_12));
  Decremento_de_1 decremento_de_1_1 (.in_1({a[2:0], b[0]}), .out_2(out_13));
  Decremento_de_1 decremento_de_1_2 (.in_1(a), .out_2(out_14));
  Produto_de_2 produto_de_2_1 (
    .in_1(a[3]), .in_2(undriven), .in_3(b[0]), .in_4(a[0]), .out_5(out_15[0]), .out_6(out_15[1]),
    .out_7(out_15[2]), .out_8(out_15[3]));
  and and_1 (out_3[0], out_3[1], somador_4bits_1_s4);
  NotExactlyOne xnor_1 (
    .out(out_6), .in0(b[0]), .in1(a[0]), .in2(a[1]), .in3(a[2]), .in5(a[0]), .in6(a[1]), .in7(a[2]),
    .in8(a[3]));

  assign b[3:1] = a[2:0];

  // Notes on the sheet:
  //   1 - Diferente
  //   Complemento de 1 b
  //   Complemento de 1 - a
  //   Complemento de 2 b
  //   Complemento de 2 a
  //   Incremento de 1 b
  //   Incremento de 1 a
  //   Decremento de 1 b
  //   Decremento de 1 a
  //   Produto de A0A1 * B0B1
  //   s0 s1 s2 s3 Carry OverFlow
  //   s0 s1 s2 s3 Comparador
  //   Comparador: 0 - A>B
  //   1 - A<=B
endmodule

module meiasoma (
  input  in_1,
  input  in_2,
  output out_3,
  output out_4
);

  and and_1 (out_4, in_2, in_1);
  xor xor_1 (out_3, in_1, in_2);
endmodule

module somacompleta (
  input  c,
  input  a,
  input  b,
  output s1,
  output s2
);

  wire meiasoma_1_out_3, meiasoma_1_out_4, meiasoma_2_out_4;

  meiasoma meiasoma_1 (.in_1(b), .in_2(a), .out_3(meiasoma_1_out_3), .out_4(meiasoma_1_out_4));
  meiasoma meiasoma_2 (.in_1(meiasoma_1_out_3), .in_2(c), .out_3(s1), .out_4(meiasoma_2_out_4));
  or or_1 (s2, meiasoma_2_out_4, meiasoma_1_out_4);
endmodule

module somador_4bits (
  input  [3:0] a,
  input  [3:0] b,
  output s0,
  output s1,
  output s2,
  output s3,
  output c,
  output s4
);

  wire somacompleta_1_s2, somacompleta_2_s2, somacompleta_3_s2;

  somacompleta somacompleta_1 (.c(1'b0), .a(a[0]), .b(b[0]), .s1(s0), .s2(somacompleta_1_s2));
  somacompleta somacompleta_2 (.c(somacompleta_1_s2), .a(a[1]), .b(b[1]), .s1(s1), .s2(somacompleta_2_s2));
  somacompleta somacompleta_3 (.c(somacompleta_2_s2), .a(a[2]), .b(b[2]), .s1(s2), .s2(somacompleta_3_s2));
  somacompleta somacompleta_4 (.c(somacompleta_3_s2), .a(a[3]), .b(b[3]), .s1(s3), .s2(c));
  not not_1 (s4, somacompleta_3_s2);
endmodule

module completamento_de_1 (
  input  [3:0] a,
  input  [3:0] b,
  output [3:0] s2,
  output [3:0] s1
);

  not not_1 (s2[0], b[0]);
  not not_2 (s2[1], b[1]);
  not not_3 (s2[2], b[2]);
  not not_4 (s2[3], b[3]);
  not not_5 (s1[0], a[0]);
  not not_6 (s1[1], a[1]);
  not not_7 (s1[2], a[2]);
  not not_8 (s1[3], a[3]);
endmodule

module \meiaDiferença  (
  input  a,
  input  b,
  output s1,
  output s2
);

  wire not_1_out;

  xor xor_1 (s1, a, b);
  not not_1 (not_1_out, a);
  and and_1 (s2, not_1_out, b);
endmodule

module diferencaCompleta (
  input  a,
  input  b,
  input  c,
  output s1,
  output s2
);

  wire \meiadiferença_1_s1 , \meiadiferença_1_s2 , \meiadiferença_2_s2 ;

  \meiaDiferença  \meiadiferença_1  (.a(a), .b(b), .s1(\meiadiferença_1_s1 ), .s2(\meiadiferença_1_s2 ));
  \meiaDiferença  \meiadiferença_2  (.a(\meiadiferença_1_s1 ), .b(c), .s1(s1), .s2(\meiadiferença_2_s2 ));
  or or_1 (s2, \meiadiferença_1_s2 , \meiadiferença_2_s2 );
endmodule

module subtrator_4bits (
  input  [3:0] in_1,
  input  [3:0] in_2,
  output [4:0] out_3
);

  wire diferencacompleta_1_s2, diferencacompleta_2_s2, diferencacompleta_3_s2;

  diferencaCompleta diferencacompleta_1 (
    .a(in_1[0]), .b(in_2[0]), .c(1'b0), .s1(out_3[4]), .s2(diferencacompleta_1_s2));
  diferencaCompleta diferencacompleta_2 (
    .a(in_1[1]), .b(in_2[1]), .c(diferencacompleta_1_s2), .s1(out_3[3]), .s2(diferencacompleta_2_s2));
  diferencaCompleta diferencacompleta_3 (
    .a(in_1[2]), .b(in_2[2]), .c(diferencacompleta_2_s2), .s1(out_3[2]), .s2(diferencacompleta_3_s2));
  diferencaCompleta diferencacompleta_4 (
    .a(in_1[3]), .b(in_2[3]), .c(diferencacompleta_3_s2), .s1(out_3[1]), .s2(out_3[0]));
endmodule

module comparador_logico (
  input  [3:0] in_1,
  input  [3:0] in_2,
  output out_3
);

  wire xor_1_out, xor_2_out, xor_3_out, xor_4_out;

  xor xor_1 (xor_1_out, in_1[0], in_2[0]);
  xor xor_2 (xor_2_out, in_1[1], in_2[1]);
  xor xor_3 (xor_3_out, in_1[2], in_2[2]);
  xor xor_4 (xor_4_out, in_1[3], in_2[3]);
  or or_1 (out_3, xor_1_out, xor_2_out, xor_3_out, xor_4_out);
endmodule

module Incremento_de_1 (
  input  [3:0] in_1,
  output [4:0] out_2
);

  somador_4bits somador_4bits_1 (
    .a(in_1), .b(4'b0001), .s0(out_2[0]), .s1(out_2[1]), .s2(out_2[2]), .s3(out_2[3]), .c(out_2[4]));  // open: s4

  // Notes on the sheet:
  //   s0 s1 s2 s3 s4
endmodule

module Decremento_de_1 (
  input  [3:0] in_1,
  output [4:0] out_2
);

  subtrator_4bits subtrator_4bits_1 (.in_1(in_1), .in_2(4'b0001), .out_3(out_2));

  // Notes on the sheet:
  //   s0 s1 s2 s3 s4
endmodule

module Complemento_de_2 (
  input  [3:0] in_1,
  output [4:0] out_2
);

  wire [3:0] completamento_de_1_1_s1;

  completamento_de_1 completamento_de_1_1 (.a(in_1), .b(4'b0000), .s1(completamento_de_1_1_s1));  // open: s2
  somador_4bits somador_4bits_1 (
    .a(completamento_de_1_1_s1), .b(4'b0001), .s0(out_2[0]), .s1(out_2[1]), .s2(out_2[2]), .s3(out_2[3]),
    .c(out_2[4]));  // open: s4

  // Notes on the sheet:
  //   s4 s3 s2 s1 s0
endmodule

module Produto_de_2 (
  input  in_1,
  input  in_2,
  input  in_3,
  input  in_4,
  output out_5,
  output out_6,
  output out_7,
  output out_8
);

  wire and_1_out, and_3_out, and_4_out, not_1_out;

  and and_1 (and_1_out, in_1, in_3);
  and and_2 (out_8, in_2, in_4);
  and and_3 (and_3_out, in_1, in_4);
  and and_4 (and_4_out, in_2, in_3);
  and and_5 (out_5, and_1_out, out_8);
  and and_6 (out_6, and_1_out, not_1_out);
  not not_1 (not_1_out, out_8);
  xor xor_1 (out_7, and_3_out, and_4_out);
endmodule
