// Logisim project Circuitos.circ as structural Verilog: 18 circuits, main circuit Meia-Soma
module Meia_Soma (
  input  a,
  input  b,
  output S0,
  output S1
);

  wire and_1_out, and_2_out, not_1_out, not_2_out;

  not not_1 (not_1_out, a);
  not not_2 (not_2_out, b);
  and and_1 (and_1_out, not_1_out, b);
  and and_2 (and_2_out, a, not_2_out);
  and and_3 (S1, a, b);
  or or_1 (S0, and_1_out, and_2_out);
endmodule

module SomaCompleta (
  input  a,
  input  b,
  input  c,
  output S0,
  output S1
);

  wire meia_soma_1_s0, meia_soma_1_s1, meia_soma_2_s1;

  Meia_Soma meia_soma_1 (.a(a), .b(b), .S0(meia_soma_1_s0), .S1(meia_soma_1_s1));
  Meia_Soma meia_soma_2 (.a(meia_soma_1_s0), .b(c), .S0(S0), .S1(meia_soma_2_s1));
  or or_1 (S1, meia_soma_2_s1, meia_soma_1_s1);
endmodule

module \Meia_Difenreça  (
  input  a,
  input  b,
  output S0,
  output S1
);

  wire and_1_out, and_2_out, not_1_out, not_2_out, not_3_out;

  not not_1 (not_1_out, a);
  not not_2 (not_2_out, b);
  not not_3 (not_3_out, a);
  and and_1 (and_1_out, not_1_out, b);
  and and_2 (and_2_out, a, not_2_out);
  and and_3 (S1, not_3_out, b);
  or or_1 (S0, and_1_out, and_2_out);
endmodule

module \DiferençaCompleta  (
  input  a,
  input  b,
  input  c,
  output S0,
  output S1
);

  wire \meia_difenreça_1_s0 , \meia_difenreça_1_s1 , \meia_difenreça_2_s1 ;

  \Meia_Difenreça  \meia_difenreça_1  (.a(a), .b(b), .S0(\meia_difenreça_1_s0 ), .S1(\meia_difenreça_1_s1 ));
  \Meia_Difenreça  \meia_difenreça_2  (.a(\meia_difenreça_1_s0 ), .b(c), .S0(S0), .S1(\meia_difenreça_2_s1 ));
  or or_1 (S1, \meia_difenreça_2_s1 , \meia_difenreça_1_s1 );
endmodule

module MeiaSoma__Nor (
  input  a,
  input  b,
  output S0,
  output S1
);

  wire nor_1_out, nor_2_out, nor_3_out, nor_4_out, nor_5_out, nor_6_out;

  nor nor_1 (nor_1_out, a, a);
  nor nor_2 (nor_2_out, b, b);
  nor nor_3 (nor_3_out, a, b);
  nor nor_4 (nor_4_out, a, a);
  nor nor_5 (nor_5_out, b, b);
  nor nor_6 (nor_6_out, nor_1_out, nor_2_out);
  nor nor_7 (S1, nor_4_out, nor_5_out);
  nor nor_8 (S0, nor_6_out, nor_3_out);
endmodule

module Somador_3bits (
  input  a2,
  input  a1,
  input  a0,
  input  b2,
  input  b1,
  input  b0,
  input  in_7,
  output S0,
  output S1,
  output S2,
  output S3
);

  wire somacompleta_1_s1, somacompleta_2_s1;

  SomaCompleta somacompleta_1 (.a(a0), .b(b0), .c(in_7), .S0(S0), .S1(somacompleta_1_s1));
  SomaCompleta somacompleta_2 (.a(a1), .b(b1), .c(somacompleta_1_s1), .S0(S1), .S1(somacompleta_2_s1));
  SomaCompleta somacompleta_3 (.a(a2), .b(b2), .c(somacompleta_2_s1), .S0(S2), .S1(S3));
endmodule

module Subtrator_2bits (
  input  a1,
  input  a0,
  input  b1,
  input  b0,
  input  in_5,
  output S0,
  output S1,
  output S2
);

  wire \diferençacompleta_1_s1 ;

  \DiferençaCompleta  \diferençacompleta_1  (.a(a0), .b(b0), .c(in_5), .S0(S0), .S1(\diferençacompleta_1_s1 ));
  \DiferençaCompleta  \diferençacompleta_2  (.a(a1), .b(b1), .c(\diferençacompleta_1_s1 ), .S0(S1), .S1(S2));
endmodule

module Multiplicador_2bits (
  input  a1,
  input  a0,
  input  b1,
  input  b0,
  input  in_5,
  output S0,
  output S1,
  output S2,
  output S3
);

  wire and_2_out, and_3_out, and_4_out, meia_soma_1_s1;

  and and_1 (S0, a0, b0);
  and and_2 (and_2_out, a0, b1);
  and and_3 (and_3_out, a1, b0);
  and and_4 (and_4_out, a1, b1);
  Meia_Soma meia_soma_1 (.a(and_2_out), .b(and_3_out), .S0(S1), .S1(meia_soma_1_s1));
  SomaCompleta somacompleta_1 (.a(and_4_out), .b(in_5), .c(meia_soma_1_s1), .S0(S2), .S1(S3));
endmodule

module ALU_0 (
  input  Sinal,
  input  a2,
  input  a1,
  input  a0,
  input  Sinal_2,
  input  b2,
  input  b1,
  input  b0,
  output Diferente,
  output S0,
  output S1,
  output S2,
  output S3,
  output Carry,
  output OVR,
  output zero,
  output a3_prime,
  output a2_prime,
  output a1_prime,
  output a0_prime,
  output b3_prime,
  output b2_prime,
  output b1_prime,
  output b0_prime,
  output S0_2,
  output S1_2,
  output S2_2,
  output S3_2,
  output Maior__Menor,
  output S0_3,
  output S1_3,
  output S2_3,
  output S3_3,
  output S4,
  output S0_4,
  output S1_4,
  output S2_4,
  output S3_4,
  output S4_2,
  output S0_5,
  output S1_5,
  output S2_5,
  output S3_5,
  output S4_3,
  output S0_6,
  output S1_6,
  output S2_6,
  output S3_6,
  output S4_4,
  output S0_7,
  output S1_7,
  output S2_7,
  output S3_7,
  output S4_5,
  output S0_8,
  output S1_8,
  output S2_8,
  output S3_8,
  output S4_6
);

  wire somador_4bits_1_c5;

  Comparador_logico comparador_logico_1 (
    .Sinal(Sinal), .a2(a2), .a1(a1), .a0(a0), .Sinal_2(Sinal_2), .b2(b2), .b1(b1), .b0(b0), .S0(Diferente));
  Somador_4bits somador_4bits_1 (
    .a3(Sinal), .a2(a2), .a1(a1), .a0(a0), .b3(Sinal_2), .b2(b2), .b1(b1), .b0(b0), .S0(S0), .S1(S1),
    .S2(S2), .S3(S3), .S4(Carry), .c5(somador_4bits_1_c5));
  Complemento_de_um complemento_de_um_1 (
    .a3(Sinal), .a2(a2), .a1(a1), .a0(a0), .a3_prime(a3_prime), .a2_prime(a2_prime), .a1_prime(a1_prime),
    .a0_prime(a0_prime));
  Complemento_de_um complemento_de_um_2 (
    .a3(Sinal_2), .a2(b2), .a1(b1), .a0(b0), .a3_prime(b3_prime), .a2_prime(b2_prime), .a1_prime(b1_prime),
    .a0_prime(b0_prime));
  Subtrator_4bits subtrator_4bits_1 (
    .a3(Sinal), .a2(a2), .a1(a1), .a0(a0), .b3(Sinal_2), .b2(b2), .b1(b1), .b0(b0), .S0(S0_2), .S1(S1_2),
    .S2(S2_2), .S3(S3_2), .Maior___menor(Maior__Menor));
  Complemento_de_dois complemento_de_dois_1 (
    .a3(Sinal), .a2(a2), .a1(a1), .a0(a0), .S0(S0_3), .S1(S1_3), .S2(S2_3), .S3(S3_3), .S4(S4));
  Complemento_de_dois complemento_de_dois_2 (
    .a3(Sinal_2), .a2(b2), .a1(b1), .a0(b0), .S0(S0_4), .S1(S1_4), .S2(S2_4), .S3(S3_4), .S4(S4_2));
  Incremento__de_um incremento__de_um_1 (
    .a3(Sinal), .a2(a2), .a1(a1), .a0(a0), .S0(S0_5), .S1(S1_5), .S2(S2_5), .S3(S3_5), .S4(S4_3));
  Incremento__de_um incremento__de_um_2 (
    .a3(Sinal_2), .a2(b2), .a1(b1), .a0(b0), .S0(S0_6), .S1(S1_6), .S2(S2_6), .S3(S3_6), .S4(S4_4));
  Decremento_de_um decremento_de_um_1 (
    .a3(Sinal), .a2(a2), .a1(a1), .a0(a0), .S0(S0_7), .S1(S1_7), .S2(S2_7), .S3(S3_7), .S4(S4_5));
  Decremento_de_um decremento_de_um_2 (
    .a3(Sinal_2), .a2(b2), .a1(b1), .a0(b0), .S0(S0_8), .S1(S1_8), .S2(S2_8), .S3(S3_8), .S4(S4_6));
  and and_1 (OVR, Carry, somador_4bits_1_c5);
  nor nor_1 (zero, b0, b1, b2, Sinal_2, a0, a1, a2, Sinal);

  // Notes on the sheet:
  //   A > B    1-Sim    0 - Não
endmodule

module Comparador_logico (
  input  Sinal,
  input  a2,
  input  a1,
  input  a0,
  input  Sinal_2,
  input  b2,
  input  b1,
  input  b0,
  output S0
);

  wire xor_1_out, xor_2_out, xor_3_out, xor_4_out;

  xor xor_1 (xor_1_out, b0, a0);
  xor xor_2 (xor_2_out, b1, a1);
  xor xor_3 (xor_3_out, b2, a2);
  xor xor_4 (xor_4_out, Sinal_2, Sinal);
  or or_1 (S0, xor_1_out, xor_2_out, xor_3_out, xor_4_out);

  // Notes on the sheet:
  //   Diferente: 1 - sim  0 - não
endmodule

module Somador_4bits (
  input  a3,
  input  a2,
  input  a1,
  input  a0,
  input  b3,
  input  b2,
  input  b1,
  input  b0,
  output S0,
  output S1,
  output S2,
  output S3,
  output S4,
  output c5
);

  wire somacompleta_1_s1, somacompleta_2_s1, somacompleta_3_s1;

  SomaCompleta somacompleta_1 (.a(a0), .b(b0), .c(1'b0), .S0(S0), .S1(somacompleta_1_s1));
  SomaCompleta somacompleta_2 (.a(a1), .b(b1), .c(somacompleta_1_s1), .S0(S1), .S1(somacompleta_2_s1));
  SomaCompleta somacompleta_3 (.a(a2), .b(b2), .c(somacompleta_2_s1), .S0(S2), .S1(somacompleta_3_s1));
  SomaCompleta somacompleta_4 (.a(a3), .b(b3), .c(somacompleta_3_s1), .S0(S3), .S1(S4));
  not not_1 (c5, somacompleta_3_s1);
endmodule

module Subtrator_4bits (
  input  a3,
  input  a2,
  input  a1,
  input  a0,
  input  b3,
  input  b2,
  input  b1,
  input  b0,
  output S0,
  output S1,
  output S2,
  output S3,
  output Maior___menor
);

  wire \diferençacompleta_1_s1 , \diferençacompleta_2_s1 , \diferençacompleta_3_s1 ;

  \DiferençaCompleta  \diferençacompleta_1  (.a(a0), .b(b0), .c(1'b0), .S0(S0), .S1(\diferençacompleta_1_s1 ));
  \DiferençaCompleta  \diferençacompleta_2  (
    .a(a1), .b(b1), .c(\diferençacompleta_1_s1 ), .S0(S1), .S1(\diferençacompleta_2_s1 ));
  \DiferençaCompleta  \diferençacompleta_3  (
    .a(a2), .b(b2), .c(\diferençacompleta_2_s1 ), .S0(S2), .S1(\diferençacompleta_3_s1 ));
  \DiferençaCompleta  \diferençacompleta_4  (.a(a3), .b(b3), .c(\diferençacompleta_3_s1 ), .S0(S3), .S1(Maior___menor));

  // Notes on the sheet:
  //   A > B    1-Sim    0 - Não
endmodule

module Complemento_de_um (
  input  a3,
  input  a2,
  input  a1,
  input  a0,
  output a3_prime,
  output a2_prime,
  output a1_prime,
  output a0_prime
);

  not not_1 (a3_prime, a3);
  not not_2 (a2_prime, a2);
  not not_3 (a1_prime, a1);
  not not_4 (a0_prime, a0);
endmodule

module Incremento__de_um (
  input  a3,
  input  a2,
  input  a1,
  input  a0,
  output S0,
  output S1,
  output S2,
  output S3,
  output S4
);

  Somador_4bits somador_4bits_1 (
    .a3(a3), .a2(a2), .a1(a1), .a0(a0), .b3(1'b0), .b2(1'b0), .b1(1'b0), .b0(1'b1), .S0(S0), .S1(S1),
    .S2(S2), .S3(S3), .S4(S4));  // open: c5
endmodule

module Decremento_de_um (
  input  a3,
  input  a2,
  input  a1,
  input  a0,
  output S0,
  output S1,
  output S2,
  output S3,
  output S4
);

  Subtrator_4bits subtrator_4bits_1 (
    .a3(a3), .a2(a2), .a1(a1), .a0(a0), .b3(1'b0), .b2(1'b0), .b1(1'b0), .b0(1'b1), .S0(S0), .S1(S1),
    .S2(S2), .S3(S3), .Maior___menor(S4));
endmodule

module Complemento_de_dois (
  input  a3,
  input  a2,
  input  a1,
  input  a0,
  output S0,
  output S1,
  output S2,
  output S3,
  output S4
);

  wire complemento_de_um_1_a0_prime, complemento_de_um_1_a1_prime, complemento_de_um_1_a2_prime,
       complemento_de_um_1_a3_prime;

  Complemento_de_um complemento_de_um_1 (
    .a3(a3), .a2(a2), .a1(a1), .a0(a0), .a3_prime(complemento_de_um_1_a3_prime),
    .a2_prime(complemento_de_um_1_a2_prime), .a1_prime(complemento_de_um_1_a1_prime),
    .a0_prime(complemento_de_um_1_a0_prime));
  Somador_4bits somador_4bits_1 (
    .a3(complemento_de_um_1_a3_prime), .a2(complemento_de_um_1_a2_prime), .a1(complemento_de_um_1_a1_prime),
    .a0(complemento_de_um_1_a0_prime), .b3(1'b0), .b2(1'b0), .b1(1'b0), .b0(1'b1), .S0(S0), .S1(S1), .S2(S2),
    .S3(S3), .S4(S4));  // open: c5
endmodule

module ALU_1 (
  input  Sinal,
  input  a2,
  input  a1,
  input  a0,
  input  Sinal_2,
  input  b2,
  input  b1,
  input  b0,
  output \Diferente____1___Sim___0___Não ,
  output [4:0] A___B,
  output [1:0] Over_flow__Zero,
  output [3:0] a_prime,
  output [3:0] b_prime,
  output [3:0] A___B_2,
  output \A___B___1___Sim___0___Não ,
  output [4:0] A___Complemento_de_2,
  output [4:0] B___Complemento_de_2,
  output [4:0] A___Incremento_de_1,
  output [4:0] B___Incremento_de_1,
  output [4:0] A___Decremento_de_1,
  output [4:0] B___Decremento_de_1
);

  ALU_0 alu_0_1 (
    .Sinal(Sinal), .a2(a2), .a1(a1), .a0(a0), .Sinal_2(Sinal_2), .b2(b2), .b1(b1), .b0(b0),
    .Diferente(\Diferente____1___Sim___0___Não ), .S0(A___B[0]), .S1(A___B[1]), .S2(A___B[2]), .S3(A___B[3]),
    .Carry(A___B[4]), .OVR(Over_flow__Zero[1]), .zero(Over_flow__Zero[0]), .a3_prime(a_prime[3]),
    .a2_prime(a_prime[2]), .a1_prime(a_prime[1]), .a0_prime(a_prime[0]), .b3_prime(b_prime[3]),
    .b2_prime(b_prime[2]), .b1_prime(b_prime[1]), .b0_prime(b_prime[0]), .S0_2(A___B_2[0]),
    .S1_2(A___B_2[1]), .S2_2(A___B_2[2]), .S3_2(A___B_2[3]), .Maior__Menor(\A___B___1___Sim___0___Não ),
    .S0_3(A___Complemento_de_2[0]), .S1_3(A___Complemento_de_2[1]), .S2_3(A___Complemento_de_2[2]),
    .S3_3(A___Complemento_de_2[3]), .S4(A___Complemento_de_2[4]), .S0_4(B___Complemento_de_2[0]),
    .S1_4(B___Complemento_de_2[1]), .S2_4(B___Complemento_de_2[2]), .S3_4(B___Complemento_de_2[3]),
    .S4_2(B___Complemento_de_2[4]), .S0_5(A___Incremento_de_1[0]), .S1_5(A___Incremento_de_1[1]),
    .S2_5(A___Incremento_de_1[2]), .S3_5(A___Incremento_de_1[3]), .S4_3(A___Incremento_de_1[4]),
    .S0_6(B___Incremento_de_1[0]), .S1_6(B___Incremento_de_1[1]), .S2_6(B___Incremento_de_1[2]),
    .S3_6(B___Incremento_de_1[3]), .S4_4(B___Incremento_de_1[4]), .S0_7(A___Decremento_de_1[0]),
    .S1_7(A___Decremento_de_1[1]), .S2_7(A___Decremento_de_1[2]), .S3_7(A___Decremento_de_1[3]),
    .S4_5(A___Decremento_de_1[4]), .S0_8(B___Decremento_de_1[0]), .S1_8(B___Decremento_de_1[1]),
    .S2_8(B___Decremento_de_1[2]), .S3_8(B___Decremento_de_1[3]), .S4_6(B___Decremento_de_1[4]));
endmodule

module ALU_2 (
  input  a0,
  input  a1,
  input  a2,
  input  Sinal,
  input  b0,
  input  b1,
  input  b2,
  input  Sinal_2,
  output \Diferente_0___Não_1___Sim ,
  output [4:0] A___B,
  output [1:0] Over_flow____Zero,
  output [3:0] a_prime,
  output [3:0] b_prime,
  output [3:0] A___B_2,
  output \A___B___1___Sim__0___Não ,
  output [4:0] A___Complemento_de_2,
  output [4:0] B___Complemento_de_2,
  output [4:0] A___Incremento_de_1,
  output [4:0] B___Incremento_de_1,
  output [4:0] A___Decremento_de_1,
  output [4:0] B___Decremento_de_1
);

  ALU_1 alu_1_1 (
    .Sinal(a0), .a2(a1), .a1(a2), .a0(Sinal), .Sinal_2(b0), .b2(b1), .b1(b2), .b0(Sinal_2),
    .\Diferente____1___Sim___0___Não (\Diferente_0___Não_1___Sim ), .A___B(A___B),
    .Over_flow__Zero(Over_flow____Zero), .a_prime(a_prime), .b_prime(b_prime), .A___B_2(A___B_2),
    .\A___B___1___Sim___0___Não (\A___B___1___Sim__0___Não ), .A___Complemento_de_2(A___Complemento_de_2),
    .B___Complemento_de_2(B___Complemento_de_2), .A___Incremento_de_1(A___Incremento_de_1),
    .B___Incremento_de_1(B___Incremento_de_1), .A___Decremento_de_1(A___Decremento_de_1),
    .B___Decremento_de_1(B___Decremento_de_1));
endmodule
