// Logisim project Guia_8.circ as structural Verilog: 3 circuits, main circuit Exemplo_01
module Exemplo_01 (
  input  a,
  input  b,
  input  c,
  input  d,
  output f
);

  wire and_1_out, and_2_out, and_3_out, not_1_out, not_2_out, not_3_out, not_4_out;

  not not_1 (not_1_out, a);
  not not_2 (not_2_out, c);
  not not_3 (not_3_out, b);
  not not_4 (not_4_out, d);
  and and_1 (and_1_out, a, b, not_4_out);
  and and_2 (and_2_out, not_1_out, c);
  and and_3 (and_3_out, not_3_out, c);
  or or_1 (f, and_1_out, and_2_out, and_3_out);

  // Notes on the sheet:
  //   Nome: Bruno Rafael Nicolletti
  //   Matrícula: 380752
endmodule

module Exemplo_02 (
  input  a,
  input  b,
  input  c,
  input  d,
  output f
);

  wire and_1_out, and_2_out, and_3_out, and_4_out, and_5_out, not_1_out, not_2_out, not_3_out, not_4_out;

  not not_1 (not_1_out, a);
  not not_2 (not_2_out, b);
  not not_3 (not_3_out, c);
  not not_4 (not_4_out, d);
  and and_1 (and_1_out, not_1_out, not_2_out, not_4_out);
  and and_2 (and_2_out, not_1_out, not_3_out, not_4_out);
  and and_3 (and_3_out, not_2_out, not_3_out, not_4_out);
  and and_4 (and_4_out, a, not_2_out, d);
  and and_5 (and_5_out, a, not_3_out, d);
  or or_1 (f, and_1_out, and_2_out, and_3_out, and_4_out, and_5_out);

  // Notes on the sheet:
  //   Nome: Bruno Rafael Nicolletti
  //   Matrícula: 380752
endmodule

module Exemplo_03 (
  input  a,
  input  b,
  input  c,
  input  d,
  input  e,
  output f
);

  wire and_1_out, and_2_out, and_3_out, and_4_out, and_5_out, and_6_out, and_7_out, not_1_out, not_2_out,
       not_3_out, not_4_out, not_5_out;

  not not_1 (not_1_out, a);
  not not_2 (not_2_out, b);
  not not_3 (not_3_out, c);
  not not_4 (not_4_out, d);
  not not_5 (not_5_out, e);
  and and_1 (and_1_out, not_1_out, not_3_out, not_4_out);
  and and_2 (and_2_out, not_2_out, not_4_out, e);
  and and_3 (and_3_out, not_2_out, c, not_4_out);
  and and_4 (and_4_out, b, c, d);
  and and_5 (and_5_out, c, e);
  and and_6 (and_6_out, a, not_2_out, not_3_out, d, not_5_out);
  and and_7 (and_7_out, a, b, d, e);
  or or_1 (f, and_6_out, and_7_out, and_1_out, and_2_out, and_3_out, and_4_out, and_5_out);

  // Notes on the sheet:
  //   Nome: Bruno Rafael Nicolletti
  //   Matrícula: 380752
endmodule
