// Logisim project guia08_ex01.circ as structural Verilog: 1 circuit, main circuit main
module main (
  input  a,
  input  b,
  input  c,
  input  d,
  output s0
);

  wire and_1_out, and_2_out, and_3_out, not_1_out, not_2_out, not_3_out;

  not not_1 (not_1_out, a);
  and and_1 (and_1_out, not_1_out, c);
  not not_2 (not_2_out, b);
  and and_2 (and_2_out, not_2_out, c);
  and and_3 (and_3_out, a, b, not_3_out);
  not not_3 (not_3_out, d);
  or or_1 (s0, and_1_out, and_2_out, and_3_out);
endmodule
