// Logisim project guia08_ex04.circ as structural Verilog: 1 circuit, main circuit main
module main (
  input  a,
  input  b,
  input  c,
  input  d,
  output s0
);

  wire nand_1_out, nand_2_out, nand_3_out, nand_4_out, nand_5_out, nand_6_out;

  nand nand_1 (nand_1_out, a, a);
  nand nand_2 (nand_2_out, b, b);
  nand nand_3 (nand_3_out, d, d);
  nand nand_4 (nand_4_out, nand_1_out, c);
  nand nand_5 (nand_5_out, nand_2_out, c);
  nand nand_6 (nand_6_out, a, b, nand_3_out);
  nand nand_7 (s0, nand_4_out, nand_5_out, nand_6_out);
endmodule
