// Logisim project guia08.circ as structural Verilog: 8 circuits, main circuit exer01
module exer01 (
  input  a,
  input  b,
  input  c,
  input  d,
  output out_5
);

  wire and_1_out, and_2_out, and_3_out, not_1_out, not_2_out, not_3_out;

  and and_1 (and_1_out, a, b, not_1_out);
  not not_1 (not_1_out, d);
  not not_2 (not_2_out, a);
  and and_2 (and_2_out, not_2_out, c);
  not not_3 (not_3_out, b);
  and and_3 (and_3_out, not_3_out, c);
  or or_1 (out_5, and_1_out, and_2_out, and_3_out);

  // Notes on the sheet:
  //   Exercicio 01
  //   Celso R França Jr
endmodule

module exer02 (
  input  a,
  input  b,
  input  c,
  input  d,
  output out_5
);

  wire and_1_out, and_2_out, and_3_out, and_4_out, and_5_out, not_4_out, not_5_out;
  wire [2:0] not_1_out, not_2_out, not_3_out;

  assign not_1_out = ~{d, b, a};  // NOT_Gate not_1, 3 bits wide
  assign not_2_out = ~{d, c, a};  // NOT_Gate not_2, 3 bits wide
  assign not_3_out = ~{d, c, b};  // NOT_Gate not_3, 3 bits wide
  not not_4 (not_4_out, b);
  not not_5 (not_5_out, c);
  and and_1 (and_1_out, not_1_out[0], not_1_out[1], not_1_out[2]);
  and and_2 (and_2_out, not_2_out[0], not_2_out[1], not_2_out[2]);
  and and_3 (and_3_out, not_3_out[0], not_3_out[1], not_3_out[2]);
  and and_4 (and_4_out, a, not_4_out, d);
  and and_5 (and_5_out, a, not_5_out, d);
  or or_1 (out_5, and_1_out, and_2_out, and_3_out, and_4_out, and_5_out);

  // Notes on the sheet:
  //   Exercicio 02
  //   Celso R França Jr
endmodule

module exer03 (
  input  a,
  input  b,
  input  c,
  input  d,
  output out_5
);

  wire and_1_out, and_2_out, and_3_out, and_4_out, and_5_out, not_3_out, not_5_out;
  wire [1:0] not_2_out;
  wire [2:0] not_1_out, not_4_out;

  assign not_1_out = ~{d, b, a};  // NOT_Gate not_1, 3 bits wide
  assign not_2_out = ~{c, b};  // NOT_Gate not_2, 2 bits wide
  not not_3 (not_3_out, c);
  assign not_4_out = ~{d, c, a};  // NOT_Gate not_4, 3 bits wide
  not not_5 (not_5_out, b);
  and and_1 (and_1_out, not_1_out[0], not_1_out[1], not_1_out[2]);
  and and_2 (and_2_out, a, not_2_out[0], not_2_out[1]);
  and and_3 (and_3_out, a, not_3_out, d);
  and and_4 (and_4_out, not_4_out[0], not_4_out[1], not_4_out[2]);
  and and_5 (and_5_out, a, not_5_out, d);
  or or_1 (out_5, and_1_out, and_2_out, and_3_out, and_4_out, and_5_out);

  // Notes on the sheet:
  //   Exercicio 03
  //   Celso R França Jr
endmodule

module exer04 (
  input  a,
  input  b,
  input  c,
  input  d,
  output out_5
);

  wire nand_1_out, nand_2_out, nand_3_out, nand_4_out, nand_5_out, nand_6_out;

  nand nand_1 (nand_1_out, d, d);
  nand nand_2 (nand_2_out, a, a);
  nand nand_3 (nand_3_out, b, b);
  nand nand_4 (nand_4_out, a, b, nand_1_out);
  nand nand_5 (nand_5_out, nand_2_out, c);
  nand nand_6 (nand_6_out, nand_3_out, c);
  nand nand_7 (out_5, nand_4_out, nand_5_out, nand_6_out);

  // Notes on the sheet:
  //   Exercicio 04
  //   Celso R França Jr
endmodule

module exer05 (
  input  a,
  input  b,
  input  c,
  input  d,
  output out_5
);

  wire and_nor_3bits_1_out_4, and_nor_3bits_2_out_4, and_nor_3bits_3_out_4, and_nor_3bits_4_out_4,
       and_nor_3bits_5_out_4, not_nor_3_bits_1_out_4, not_nor_3_bits_1_out_5, not_nor_3_bits_1_out_6,
       not_nor_3_bits_2_out_4, not_nor_3_bits_2_out_5, not_nor_3_bits_2_out_6, not_nor_3_bits_3_out_4,
       not_nor_3_bits_3_out_5, not_nor_3_bits_3_out_6, not_nor_3_bits_4_out_5, not_nor_3_bits_5_out_5;

  not__nor__3_bits not_nor_3_bits_1 (
    .in_1(a), .in_2(b), .in_3(d), .out_4(not_nor_3_bits_1_out_4), .out_5(not_nor_3_bits_1_out_5),
    .out_6(not_nor_3_bits_1_out_6));
  not__nor__3_bits not_nor_3_bits_2 (
    .in_1(a), .in_2(b), .in_3(d), .out_4(not_nor_3_bits_2_out_4), .out_5(not_nor_3_bits_2_out_5),
    .out_6(not_nor_3_bits_2_out_6));
  not__nor__3_bits not_nor_3_bits_3 (
    .in_1(b), .in_2(c), .in_3(d), .out_4(not_nor_3_bits_3_out_4), .out_5(not_nor_3_bits_3_out_5),
    .out_6(not_nor_3_bits_3_out_6));
  not__nor__3_bits not_nor_3_bits_4 (.in_2(b), .out_5(not_nor_3_bits_4_out_5));  // open: in_1, in_3, out_4, out_6
  not__nor__3_bits not_nor_3_bits_5 (.in_2(c), .out_5(not_nor_3_bits_5_out_5));  // open: in_1, in_3, out_4, out_6
  and_nor_3bits and_nor_3bits_1 (
    .in_1(not_nor_3_bits_1_out_4), .in_2(not_nor_3_bits_1_out_5), .in_3(not_nor_3_bits_1_out_6),
    .out_4(and_nor_3bits_1_out_4));
  and_nor_3bits and_nor_3bits_2 (
    .in_1(not_nor_3_bits_2_out_4), .in_2(not_nor_3_bits_2_out_5), .in_3(not_nor_3_bits_2_out_6),
    .out_4(and_nor_3bits_2_out_4));
  and_nor_3bits and_nor_3bits_3 (
    .in_1(not_nor_3_bits_3_out_4), .in_2(not_nor_3_bits_3_out_5), .in_3(not_nor_3_bits_3_out_6),
    .out_4(and_nor_3bits_3_out_4));
  and_nor_3bits and_nor_3bits_4 (.in_1(a), .in_2(not_nor_3_bits_4_out_5), .in_3(d), .out_4(and_nor_3bits_4_out_4));
  and_nor_3bits and_nor_3bits_5 (.in_1(a), .in_2(not_nor_3_bits_5_out_5), .in_3(d), .out_4(and_nor_3bits_5_out_4));
  or_nor or_nor_1 (
    .in_1(and_nor_3bits_1_out_4), .in_2(and_nor_3bits_2_out_4), .in_3(and_nor_3bits_3_out_4),
    .in_4(and_nor_3bits_4_out_4), .in_5(and_nor_3bits_5_out_4), .out_6(out_5));

  // Notes on the sheet:
  //   Exercicio 05
  //   Celso R França Jr
endmodule

module and_nor_3bits (
  input  in_1,
  input  in_2,
  input  in_3,
  output out_4
);

  wire nor_1_out, nor_2_out, nor_3_out;

  nor nor_1 (nor_1_out, in_1, in_1);
  nor nor_2 (nor_2_out, in_2, in_2);
  nor nor_3 (nor_3_out, in_3, in_3);
  nor nor_4 (out_4, nor_1_out, nor_2_out, nor_3_out);

  // Notes on the sheet:
  //   and(nor) - 3 bits
endmodule

module not__nor__3_bits (
  input  in_1,
  input  in_2,
  input  in_3,
  output out_4,
  output out_5,
  output out_6
);

  nor nor_1 (out_4, in_1, in_1);
  nor nor_2 (out_5, in_2, in_2);
  nor nor_3 (out_6, in_3, in_3);
endmodule

module or_nor (
  input  in_1,
  input  in_2,
  input  in_3,
  input  in_4,
  input  in_5,
  output out_6
);

  wire nor_1_out;

  nor nor_1 (nor_1_out, in_1, in_2, in_3, in_4, in_5);
  nor nor_2 (out_6, nor_1_out, nor_1_out);
endmodule
