// Logisim project circuito.circ as structural Verilog: 6 circuits, main circuit Exercicio1
module Exercicio1 (
  input  a,
  input  b,
  input  c,
  input  d,
  output s0
);

  wire and_1_out, and_2_out, and_3_out, and_4_out, not_1_out, not_2_out, not_3_out;

  not not_1 (not_1_out, d);
  not not_2 (not_2_out, b);
  not not_3 (not_3_out, a);
  and and_1 (and_1_out, a, b, not_1_out);
  and and_2 (and_2_out, c, not_1_out);
  and and_3 (and_3_out, not_2_out, c);
  and and_4 (and_4_out, not_3_out, c);
  or or_1 (s0, and_1_out, and_2_out, and_3_out, and_4_out);

  // Notes on the sheet:
  //   Márcia Cibele Martins Carneiro - 404591
endmodule

module Exercicio2 (
  input  a,
  input  b,
  input  c,
  input  d,
  output S1
);

  wire and_1_out, and_2_out, and_3_out, and_4_out, and_5_out, not_1_out, not_2_out, not_3_out, not_4_out,
       not_5_out, not_6_out, not_7_out, not_8_out, not_9_out, not_10_out, not_11_out;

  not not_1 (not_1_out, a);
  not not_2 (not_2_out, b);
  not not_3 (not_3_out, d);
  not not_4 (not_4_out, a);
  not not_5 (not_5_out, c);
  not not_6 (not_6_out, d);
  not not_7 (not_7_out, b);
  not not_8 (not_8_out, c);
  not not_9 (not_9_out, d);
  not not_10 (not_10_out, b);
  not not_11 (not_11_out, c);
  and and_1 (and_1_out, not_1_out, not_2_out, not_3_out);
  and and_2 (and_2_out, not_4_out, not_5_out, not_6_out);
  and and_3 (and_3_out, not_7_out, not_8_out, not_9_out);
  and and_4 (and_4_out, a, not_10_out, d);
  and and_5 (and_5_out, a, not_11_out, d);
  or or_1 (S1, and_1_out, and_2_out, and_3_out, and_4_out, and_5_out);

  // Notes on the sheet:
  //   Márcia Cibele Martins Carneiro - 404591
endmodule

module Exercicio3 (
  input  a,
  input  b,
  input  c,
  input  d,
  input  e,
  output S0
);

  wire and_1_out, and_2_out, and_3_out, and_4_out, and_5_out, and_6_out, and_7_out, and_8_out, not_1_out,
       not_2_out, not_3_out, not_4_out, not_5_out;

  not not_1 (not_1_out, a);
  not not_2 (not_2_out, c);
  not not_3 (not_3_out, b);
  not not_4 (not_4_out, d);
  not not_5 (not_5_out, e);
  and and_1 (and_1_out, a, not_3_out, not_2_out, d, e);
  and and_2 (and_2_out, a, b, d, e);
  and and_3 (and_3_out, not_1_out, not_2_out, not_4_out);
  and and_4 (and_4_out, not_3_out, not_4_out, not_5_out);
  and and_5 (and_5_out, not_3_out, c, not_4_out);
  and and_6 (and_6_out, c, d, e);
  and and_7 (and_7_out, b, c, e);
  and and_8 (and_8_out, b, c, d);
  or or_1 (S0, and_1_out, and_2_out, and_3_out, and_4_out, and_5_out, and_6_out, and_7_out, and_8_out);

  // Notes on the sheet:
  //   Márcia Cibele Martins Carneiro - 404591
endmodule

module Exercicio4 (
  input  a,
  input  b,
  input  c,
  input  d,
  output s0
);

  wire nand_1_out, nand_2_out, nand_3_out, nand_4_out, nand_5_out, nand_6_out;

  nand nand_1 (nand_1_out, a, a);
  nand nand_2 (nand_2_out, b, b);
  nand nand_3 (nand_3_out, d, d);
  nand nand_4 (nand_4_out, nand_1_out, c);
  nand nand_5 (nand_5_out, nand_2_out, c);
  nand nand_6 (nand_6_out, a, b, nand_3_out);
  nand nand_7 (s0, nand_4_out, nand_5_out, nand_6_out);

  // Notes on the sheet:
  //   Márcia Cibele Martins Carneiro - 404591
endmodule

module Exercicio5 (
  input  a,
  input  b,
  input  c,
  input  d,
  output s0
);

  wire nor_1_out, nor_2_out, nor_3_out, nor_4_out, nor_5_out, nor_6_out, nor_7_out, nor_8_out, nor_9_out,
       nor_10_out, nor_11_out, nor_12_out, nor_13_out, nor_14_out, nor_15_out, nor_16_out, nor_17_out,
       nor_18_out, nor_19_out, nor_20_out, nor_21_out, nor_22_out, nor_23_out, nor_24_out, nor_25_out,
       nor_26_out, nor_27_out, nor_28_out, nor_29_out, nor_30_out, nor_31_out, nor_32_out;

  nor nor_1 (nor_1_out, a, a);
  nor nor_2 (nor_2_out, b, b);
  nor nor_3 (nor_3_out, d, d);
  nor nor_4 (nor_4_out, a, a);
  nor nor_5 (nor_5_out, c, c);
  nor nor_6 (nor_6_out, d, d);
  nor nor_7 (nor_7_out, b, b);
  nor nor_8 (nor_8_out, c, c);
  nor nor_9 (nor_9_out, d, d);
  nor nor_10 (nor_10_out, a, a);
  nor nor_11 (nor_11_out, b, b);
  nor nor_12 (nor_12_out, d, d);
  nor nor_13 (nor_13_out, a, a);
  nor nor_14 (nor_14_out, c, c);
  nor nor_15 (nor_15_out, d, d);
  nor nor_16 (nor_16_out, nor_1_out, nor_1_out);
  nor nor_17 (nor_17_out, nor_2_out, nor_2_out);
  nor nor_18 (nor_18_out, nor_3_out, nor_3_out);
  nor nor_19 (nor_19_out, nor_4_out, nor_4_out);
  nor nor_20 (nor_20_out, nor_5_out, nor_5_out);
  nor nor_21 (nor_21_out, nor_6_out, nor_6_out);
  nor nor_22 (nor_22_out, nor_7_out, nor_7_out);
  nor nor_23 (nor_23_out, nor_8_out, nor_8_out);
  nor nor_24 (nor_24_out, nor_9_out, nor_9_out);
  nor nor_25 (nor_25_out, nor_11_out, nor_11_out);
  nor nor_26 (nor_26_out, nor_14_out, nor_14_out);
  nor nor_27 (nor_27_out, nor_16_out, nor_17_out, nor_18_out);
  nor nor_28 (nor_28_out, nor_19_out, nor_20_out, nor_21_out);
  nor nor_29 (nor_29_out, nor_22_out, nor_23_out, nor_24_out);
  nor nor_30 (nor_30_out, nor_10_out, nor_25_out, nor_12_out);
  nor nor_31 (nor_31_out, nor_13_out, nor_26_out, nor_15_out);
  nor nor_32 (nor_32_out, nor_27_out, nor_28_out, nor_29_out, nor_30_out, nor_31_out);
  nor nor_33 (s0, nor_32_out, nor_32_out);

  // Notes on the sheet:
  //   Márcia Cibele Martins Carneiro - 404591
endmodule

module main (
  input  a,
  input  b,
  input  c,
  input  d,
  input  e,
  output Exercicio1,
  output Exercicio2,
  output Exercicio3,
  output Exercicio4,
  output Exercicio5
);

  Exercicio1 exercicio1_1 (.a(a), .b(b), .c(c), .d(d), .s0(Exercicio1));
  Exercicio2 exercicio2_1 (.a(a), .b(b), .c(c), .d(d), .S1(Exercicio2));
  Exercicio3 exercicio3_1 (.a(a), .b(b), .c(c), .d(d), .e(e), .S0(Exercicio3));
  Exercicio4 exercicio4_1 (.a(a), .b(b), .c(c), .d(d), .s0(Exercicio4));
  Exercicio5 exercicio5_1 (.a(a), .b(b), .c(c), .d(d), .s0(Exercicio5));

  // Notes on the sheet:
  //   Márcia Cibele Martins Carneiro - 404591
endmodule
