// Logisim project G8E1.circ as structural Verilog: 1 circuit, main circuit main
module main (
  input  a,
  input  b,
  input  c,
  input  d,
  output Out
);

  wire and_1_out, and_2_out, and_3_out, and_4_out, not_1_out, not_2_out, not_3_out;

  not not_1 (not_1_out, d);
  not not_2 (not_2_out, a);
  and and_1 (and_1_out, not_2_out, c);
  not not_3 (not_3_out, b);
  and and_2 (and_2_out, not_3_out, c);
  and and_3 (and_3_out, c, not_1_out);
  and and_4 (and_4_out, b, not_1_out, a);
  or or_1 (Out, and_1_out, and_2_out, and_3_out, and_4_out);

  // Notes on the sheet:
  //   Matrícula:405782
  //   Guia 08_01 - Σm( 2, 3, 6, 7, 10, 11, 12, 14 )
  //   Nome: Alan Diniz Nogueira Machado
endmodule
