// Logisim project G8E2.circ as structural Verilog: 1 circuit, main circuit main
module main (
  input  a,
  input  b,
  input  c,
  input  d,
  output Out
);

  wire and_1_out, and_2_out, and_3_out, and_4_out, and_5_out, and_6_out, not_1_out, not_2_out, not_3_out,
       not_4_out;

  not not_1 (not_1_out, b);
  not not_2 (not_2_out, c);
  not not_3 (not_3_out, d);
  and and_1 (and_1_out, not_1_out, not_2_out, not_3_out);
  not not_4 (not_4_out, a);
  and and_2 (and_2_out, not_2_out, not_4_out, not_3_out);
  and and_3 (and_3_out, not_4_out, not_1_out, not_3_out);
  and and_4 (and_4_out, a, not_1_out, not_2_out);
  and and_5 (and_5_out, a, not_2_out, d);
  and and_6 (and_6_out, a, not_1_out, d);
  or or_1 (Out, and_1_out, and_2_out, and_3_out, and_4_out, and_5_out, and_6_out);

  // Notes on the sheet:
  //   Matrícula:405782
  //   Guia 08_02 - Σm( 0, 2, 4, 8, 9, 11, 13 )
  //   Nome: Alan Diniz Nogueira Machado
endmodule
