// Logisim project G8E3.circ as structural Verilog: 1 circuit, main circuit main
module main (
  input  a,
  input  b,
  input  c,
  input  d,
  input  e,
  output Out
);

  wire and_1_out, and_2_out, and_3_out, and_4_out, and_5_out, and_6_out, and_7_out, and_8_out, and_9_out,
       not_1_out, not_2_out, not_3_out, not_4_out, not_5_out, not_6_out, not_7_out, not_8_out, not_9_out;

  not not_1 (not_1_out, a);
  not not_2 (not_2_out, c);
  not not_3 (not_3_out, d);
  not not_4 (not_4_out, b);
  not not_5 (not_5_out, a);
  not not_6 (not_6_out, d);
  not not_7 (not_7_out, e);
  and and_1 (and_1_out, c, e);
  and and_2 (and_2_out, not_1_out, not_2_out, not_3_out);
  and and_3 (and_3_out, not_1_out, not_4_out, not_3_out);
  and and_4 (and_4_out, not_4_out, not_3_out, c);
  and and_5 (and_5_out, c, b, d);
  and and_6 (and_6_out, e, not_4_out, not_6_out);
  and and_7 (and_7_out, not_5_out, not_6_out, e);
  and and_8 (and_8_out, a, b, d, e);
  not not_8 (not_8_out, b);
  and and_9 (and_9_out, a, not_8_out, not_9_out, d, not_7_out);
  not not_9 (not_9_out, c);
  or or_1 (Out, and_1_out, and_2_out, and_3_out, and_4_out, and_5_out, and_6_out, and_7_out, and_8_out, and_9_out);

  // Notes on the sheet:
  //   Guia 08_03
  //   Matrícula:405782
  //   Nome: Alan Diniz Nogueira Machado
endmodule
