// Logisim project guia8.circ as structural Verilog: 3 circuits, main circuit Exercício 1
module \Exercício_1  (
  input  [3:0] ABCD,
  output S
);

  wire and_1_out, and_2_out, and_3_out, not_1_out, not_2_out, not_3_out;

  not not_1 (not_1_out, ABCD[0]);
  not not_2 (not_2_out, ABCD[3]);
  not not_3 (not_3_out, ABCD[2]);
  and and_1 (and_1_out, ABCD[3], ABCD[2], not_1_out);
  and and_2 (and_2_out, not_2_out, ABCD[1]);
  and and_3 (and_3_out, not_3_out, ABCD[1]);
  or or_1 (S, and_1_out, and_2_out, and_3_out);

  // Notes on the sheet:
  //   Nome: Daniel Sathler Silva   Matríula: 405795
endmodule

module Exercicio_2 (
  input  [3:0] ABCD,
  output S
);

  wire and_1_out, and_2_out, and_3_out, and_4_out, and_5_out;
  wire [3:0] not_1_out;

  assign not_1_out = ~ABCD;  // NOT_Gate not_1, 4 bits wide
  and and_1 (and_1_out, not_1_out[3], not_1_out[2], not_1_out[0]);
  and and_2 (and_2_out, not_1_out[3], not_1_out[1], not_1_out[0]);
  and and_3 (and_3_out, ABCD[3], not_1_out[2], not_1_out[1]);
  and and_4 (and_4_out, ABCD[3], not_1_out[2], ABCD[0]);
  and and_5 (and_5_out, ABCD[3], not_1_out[1], ABCD[0]);
  or or_1 (S, and_1_out, and_2_out, and_3_out, and_4_out, and_5_out);

  // Notes on the sheet:
  //   Nome: Daniel Sathler Silva   Matríula: 405795
endmodule

module \Exercício_3  (
  input  [4:0] in_1,
  output out_2
);

  wire and_1_out, and_2_out, and_3_out, and_4_out, and_5_out, and_6_out;
  wire [4:0] not_1_out;

  assign not_1_out = ~in_1;  // NOT_Gate not_1, 5 bits wide
  and and_1 (and_1_out, in_1[4], in_1[3], in_1[1], in_1[0]);
  and and_2 (and_2_out, not_1_out[4], not_1_out[2], not_1_out[1]);
  and and_3 (and_3_out, not_1_out[3], in_1[2], not_1_out[1]);
  and and_4 (and_4_out, in_1[3], in_1[2], in_1[1]);
  and and_5 (and_5_out, not_1_out[3], not_1_out[1], in_1[0]);
  and and_6 (and_6_out, in_1[2], in_1[0]);
  or or_1 (out_2, and_1_out, and_2_out, and_3_out, and_4_out, and_5_out, and_6_out);

  // Notes on the sheet:
  //   Nome: Daniel Sathler Silva   Matríula: 405795
endmodule
