// Logisim project Guia8.circ as structural Verilog
module Exercicio_01 (
  input  a,
  input  b,
  input  c,
  input  d,
  output s1
);

  wire and_1_out, and_2_out, and_3_out, not_1_out, not_2_out, not_3_out;

  not not_1 (not_1_out, a);
  not not_2 (not_2_out, b);
  not not_3 (not_3_out, d);
  and and_1 (and_1_out, not_3_out, b, a);
  and and_2 (and_2_out, not_1_out, c);
  and and_3 (and_3_out, not_2_out, c);
  or or_1 (s1, and_1_out, and_2_out, and_3_out);

  // Notes on the sheet:
  //   Nome: Gustavo Guimarães
  //   Matricula: 405804
endmodule

module Exercicio_02 (
  input  a,
  input  b,
  input  c,
  input  d,
  output out_5
);

  wire and_1_out, and_2_out, and_3_out, and_4_out, and_5_out, not_1_out, not_2_out, not_3_out, not_4_out;

  not not_1 (not_1_out, a);
  not not_2 (not_2_out, b);
  not not_3 (not_3_out, c);
  not not_4 (not_4_out, d);
  and and_1 (and_1_out, not_4_out, not_2_out, not_1_out);
  and and_2 (and_2_out, not_4_out, not_3_out, not_1_out);
  and and_3 (and_3_out, not_3_out, not_2_out, a);
  and and_4 (and_4_out, d, not_2_out, a);
  and and_5 (and_5_out, d, not_3_out, a);
  or or_1 (out_5, and_1_out, and_2_out, and_3_out, and_4_out, and_5_out);

  // Notes on the sheet:
  //   Nome: Gustavo Guimarães
  //   Matricula: 405804
endmodule

module Exercicio_03 (
  input  a,
  input  b,
  input  c,
  input  d,
  input  e,
  output s3
);

  wire and_1_out, and_2_out, and_3_out, and_4_out, and_5_out, and_6_out, not_1_out, not_2_out, not_3_out,
       not_4_out;

  not not_1 (not_1_out, a);
  not not_2 (not_2_out, b);
  not not_3 (not_3_out, d);
  not not_4 (not_4_out, c);
  and and_1 (and_1_out, e, d, b, a);
  and and_2 (and_2_out, not_3_out, not_4_out, not_1_out);
  and and_3 (and_3_out, not_3_out, c, not_2_out);
  and and_4 (and_4_out, d, c, b);
  and and_5 (and_5_out, e, not_3_out, not_2_out);
  and and_6 (and_6_out, e, c);
  or or_1 (s3, and_1_out, and_2_out, and_3_out, and_4_out, and_5_out, and_6_out);

  // Notes on the sheet:
  //   Nome: Gustavo Guimarães
  //   Matricula: 405804
endmodule
