// Logisim project guia_08.circ as structural Verilog: 5 circuits, main circuit ex_01
module ex_01 (
  input  a,
  input  b,
  input  c,
  input  d,
  output out_5
);

  wire and_1_out, and_2_out, and_3_out, not_1_out, not_2_out, not_3_out, not_4_out;

  not not_1 (not_1_out, a);
  not not_2 (not_2_out, b);
  not not_3 (not_3_out, c);
  not not_4 (not_4_out, d);
  and and_1 (and_1_out, a, not_2_out, c);
  and and_2 (and_2_out, a, b, not_4_out);
  and and_3 (and_3_out, not_1_out, c);
  or or_1 (out_5, and_1_out, and_2_out, and_3_out);

  // Notes on the sheet:
  //   José Erimá F. Júnior
  //   ab'c + abd' + a'c
endmodule

module ex_02 (
  input  a,
  input  b,
  input  c,
  input  d,
  output out_5
);

  wire and_1_out, and_2_out, not_1_out, not_2_out, not_3_out, not_4_out;

  not not_1 (not_1_out, a);
  not not_2 (not_2_out, b);
  not not_3 (not_3_out, d);
  not not_4 (not_4_out, c);
  and and_1 (and_1_out, not_2_out, not_4_out, not_3_out);
  and and_2 (and_2_out, a, not_2_out, d);
  or or_1 (out_5, and_1_out, not_4_out, and_2_out);

  // Notes on the sheet:
  //   c' + b'c'd' + ab'd
endmodule

module ex_03 (
  input  a,
  input  b,
  input  c,
  input  d,
  input  e,
  output out_6
);

  wire and_1_out, and_2_out, and_3_out, not_1_out, not_2_out, not_3_out, not_4_out;

  not not_1 (not_1_out, a);
  not not_2 (not_2_out, b);
  not not_3 (not_3_out, d);
  not not_4 (not_4_out, c);
  and and_1 (and_1_out, not_1_out, not_4_out, d);
  and and_2 (and_2_out, not_2_out, not_3_out, e);
  and and_3 (and_3_out, c, e);
  or or_1 (out_6, and_1_out, c, and_2_out, and_3_out);

  // Notes on the sheet:
  //   c + a'c'd + b'd'e' + ce
endmodule

module ex_04 (
  input  a,
  input  b,
  input  c,
  input  d,
  output out_5
);

  wire nand_1_out, nand_2_out, nand_3_out, nand_4_out, nand_5_out, nand_6_out, nand_7_out, nand_8_out,
       nand_9_out, not_1_out, not_2_out, not_3_out, not_4_out;

  not not_1 (not_1_out, a);
  not not_2 (not_2_out, b);
  not not_3 (not_3_out, c);
  not not_4 (not_4_out, d);
  nand nand_1 (nand_1_out, a, not_2_out, c);
  nand nand_2 (nand_2_out, a, b, not_4_out);
  nand nand_3 (nand_3_out, not_1_out, c);
  nand nand_4 (nand_4_out, nand_1_out, nand_1_out);
  nand nand_5 (nand_5_out, nand_2_out, nand_2_out);
  nand nand_6 (nand_6_out, nand_3_out, nand_3_out);
  nand nand_7 (nand_7_out, nand_4_out, nand_4_out);
  nand nand_8 (nand_8_out, nand_5_out, nand_5_out);
  nand nand_9 (nand_9_out, nand_6_out, nand_6_out);
  nand nand_10 (out_5, nand_7_out, nand_8_out, nand_9_out);
endmodule

module ex_05 (
  input  a,
  input  b,
  input  c,
  input  d,
  output out_5
);

  wire nor_1_out, nor_2_out, nor_3_out, nor_4_out, nor_5_out, nor_6_out, nor_7_out, nor_8_out, nor_9_out,
       not_1_out, not_2_out, not_3_out, not_4_out;

  not not_1 (not_1_out, a);
  not not_2 (not_2_out, c);
  not not_3 (not_3_out, b);
  not not_4 (not_4_out, d);
  nor nor_1 (nor_1_out, not_3_out, not_3_out);
  nor nor_2 (nor_2_out, not_2_out, not_2_out);
  nor nor_3 (nor_3_out, not_4_out, not_4_out);
  nor nor_4 (nor_4_out, a, a);
  nor nor_5 (nor_5_out, not_3_out, not_3_out);
  nor nor_6 (nor_6_out, d, d);
  nor nor_7 (nor_7_out, nor_1_out, nor_2_out, nor_3_out);
  nor nor_8 (nor_8_out, nor_4_out, nor_5_out, nor_6_out);
  nor nor_9 (nor_9_out, nor_7_out, not_2_out, nor_8_out);
  nor nor_10 (out_5, nor_9_out, nor_9_out);
endmodule
