// Logisim project Guia08_01.circ as structural Verilog: 1 circuit, main circuit main
module main (
  input  a,
  input  b,
  input  c,
  input  d,
  output s
);

  wire and_1_out, and_2_out, and_3_out, not_1_out, not_2_out, not_3_out;

  not not_1 (not_1_out, a);
  not not_2 (not_2_out, d);
  not not_3 (not_3_out, b);
  and and_1 (and_1_out, not_1_out, c, d);
  and and_2 (and_2_out, a, b, not_2_out);
  and and_3 (and_3_out, not_3_out, c);
  or or_1 (s, and_1_out, and_2_out, and_3_out);

  // Notes on the sheet:
  //                                     Luiz Felipe Fonseca - 405817
endmodule
