// Logisim project 405820_Circuitos_para_Logisim.circ as structural Verilog: 6 circuits, main circuit main
module main (
  input  a,
  input  b,
  input  c,
  input  d,
  input  e,
  output numero_01,
  output numero_02,
  output numero_04,
  output numero_03,
  output numero_05
);

  numero_01 numero_01_1 (.a(a), .b(b), .c(c), .d(d), .s(numero_01));
  numero_02 numero_02_1 (.a(a), .b(b), .c(c), .d(d), .s(numero_02));
  numero_03 numero_03_1 (.a(a), .b(b), .c(c), .d(d), .e(e), .s(numero_03));
  numero_04 numero_04_1 (.a(a), .b(b), .c(c), .d(d), .s(numero_04));
  numero_05 numero_05_1 (.a(a), .b(b), .c(c), .d(d), .s(numero_05));
endmodule

module numero_01 (
  input  a,
  input  b,
  input  c,
  input  d,
  output s
);

  wire and_1_out, and_2_out, and_3_out, not_1_out, not_2_out, not_3_out;

  not not_1 (not_1_out, d);
  not not_2 (not_2_out, a);
  not not_3 (not_3_out, b);
  and and_1 (and_1_out, a, b, not_1_out);
  and and_2 (and_2_out, not_2_out, c);
  and and_3 (and_3_out, not_3_out, c);
  or or_1 (s, and_1_out, and_2_out, and_3_out);
endmodule

module numero_02 (
  input  a,
  input  b,
  input  c,
  input  d,
  output s
);

  wire and_1_out, and_2_out, and_3_out, and_4_out, and_5_out, not_1_out, not_2_out, not_3_out, not_4_out,
       not_5_out, not_6_out, not_7_out, not_8_out, not_9_out, not_10_out, not_11_out;

  not not_1 (not_1_out, b);
  not not_2 (not_2_out, c);
  not not_3 (not_3_out, a);
  not not_4 (not_4_out, b);
  not not_5 (not_5_out, d);
  not not_6 (not_6_out, a);
  not not_7 (not_7_out, c);
  not not_8 (not_8_out, d);
  not not_9 (not_9_out, b);
  not not_10 (not_10_out, c);
  not not_11 (not_11_out, d);
  and and_1 (and_1_out, a, not_1_out, d);
  and and_2 (and_2_out, a, not_2_out, d);
  and and_3 (and_3_out, not_3_out, not_4_out, not_5_out);
  and and_4 (and_4_out, not_6_out, not_7_out, not_8_out);
  and and_5 (and_5_out, not_9_out, not_10_out, not_11_out);
  or or_1 (s, and_3_out, and_4_out, and_5_out, and_1_out, and_2_out);
endmodule

module numero_03 (
  input  a,
  input  b,
  input  c,
  input  d,
  input  e,
  output s
);

  wire and_1_out, and_2_out, and_3_out, and_4_out, and_5_out, and_6_out, and_7_out, not_1_out, not_2_out,
       not_3_out, not_4_out, not_5_out, not_6_out, not_7_out, not_8_out, not_9_out, not_10_out;

  not not_1 (not_1_out, a);
  not not_2 (not_2_out, c);
  not not_3 (not_3_out, d);
  not not_4 (not_4_out, b);
  not not_5 (not_5_out, d);
  not not_6 (not_6_out, b);
  not not_7 (not_7_out, d);
  not not_8 (not_8_out, b);
  not not_9 (not_9_out, c);
  not not_10 (not_10_out, e);
  and and_1 (and_1_out, a, b, d, e);
  and and_2 (and_2_out, not_1_out, not_2_out, not_3_out);
  and and_3 (and_3_out, not_4_out, not_5_out, e);
  and and_4 (and_4_out, not_6_out, not_7_out, c);
  and and_5 (and_5_out, b, c, d);
  and and_6 (and_6_out, c, e);
  and and_7 (and_7_out, not_8_out, a, not_9_out, d, not_10_out);
  or or_1 (s, and_1_out, and_2_out, and_3_out, and_4_out, and_5_out, and_6_out, and_7_out);
endmodule

module numero_04 (
  input  a,
  input  b,
  input  c,
  input  d,
  output s
);

  wire nand_1_out, nand_2_out, nand_3_out, nand_4_out, nand_5_out, nand_6_out, nand_7_out, nand_8_out,
       nand_9_out, nand_10_out, nand_11_out, nand_12_out;

  nand nand_1 (nand_1_out, d, d);
  nand nand_2 (nand_2_out, a, a);
  nand nand_3 (nand_3_out, b, b);
  nand nand_4 (nand_4_out, a, b, nand_1_out);
  nand nand_5 (nand_5_out, c, nand_2_out);
  nand nand_6 (nand_6_out, c, nand_3_out);
  nand nand_7 (nand_7_out, nand_4_out, nand_4_out);
  nand nand_8 (nand_8_out, nand_5_out, nand_5_out);
  nand nand_9 (nand_9_out, nand_6_out, nand_6_out);
  nand nand_10 (nand_10_out, nand_8_out, nand_8_out);
  nand nand_11 (nand_11_out, nand_7_out, nand_7_out);
  nand nand_12 (nand_12_out, nand_9_out, nand_9_out);
  nand nand_13 (s, nand_11_out, nand_10_out, nand_12_out);
endmodule

module numero_05 (
  input  a,
  input  b,
  input  c,
  input  d,
  output s
);

  wire nor_1_out, nor_2_out, nor_3_out, nor_4_out, nor_5_out, nor_6_out, nor_7_out, nor_8_out, nor_9_out,
       nor_10_out, nor_11_out, nor_12_out, nor_13_out, nor_14_out, nor_15_out, nor_16_out, nor_17_out,
       nor_18_out, nor_19_out, nor_20_out, nor_21_out, nor_22_out, nor_23_out, nor_24_out, nor_25_out,
       nor_26_out, nor_27_out, nor_28_out, nor_29_out, nor_30_out, nor_31_out, nor_32_out;

  nor nor_1 (nor_1_out, a, a);
  nor nor_2 (nor_2_out, b, b);
  nor nor_3 (nor_3_out, nor_2_out, nor_2_out);
  nor nor_4 (nor_4_out, d, d);
  nor nor_5 (nor_5_out, a, a);
  nor nor_6 (nor_6_out, c, c);
  nor nor_7 (nor_7_out, nor_6_out, nor_6_out);
  nor nor_8 (nor_8_out, d, d);
  nor nor_9 (nor_9_out, b, b);
  nor nor_10 (nor_10_out, nor_11_out, nor_11_out);
  nor nor_11 (nor_11_out, c, c);
  nor nor_12 (nor_12_out, d, d);
  nor nor_13 (nor_13_out, nor_14_out, nor_14_out);
  nor nor_14 (nor_14_out, b, b);
  nor nor_15 (nor_15_out, c, c);
  nor nor_16 (nor_16_out, nor_15_out, nor_15_out);
  nor nor_17 (nor_17_out, nor_1_out, nor_1_out);
  nor nor_18 (nor_18_out, nor_4_out, nor_4_out);
  nor nor_19 (nor_19_out, nor_5_out, nor_5_out);
  nor nor_20 (nor_20_out, nor_8_out, nor_8_out);
  nor nor_21 (nor_21_out, nor_9_out, nor_9_out);
  nor nor_22 (nor_22_out, nor_12_out, nor_12_out);
  nor nor_23 (nor_23_out, a, a);
  nor nor_24 (nor_24_out, d, d);
  nor nor_25 (nor_25_out, a, a);
  nor nor_26 (nor_26_out, d, d);
  nor nor_27 (nor_27_out, nor_17_out, nor_3_out, nor_18_out);
  nor nor_28 (nor_28_out, nor_19_out, nor_7_out, nor_20_out);
  nor nor_29 (nor_29_out, nor_21_out, nor_10_out, nor_22_out);
  nor nor_30 (nor_30_out, nor_23_out, nor_13_out, nor_24_out);
  nor nor_31 (nor_31_out, nor_25_out, nor_16_out, nor_26_out);
  nor nor_32 (nor_32_out, nor_27_out, nor_28_out, nor_29_out, nor_30_out, nor_31_out);
  nor nor_33 (s, nor_32_out, nor_32_out);
endmodule
