// Logisim project Exercicio01.circ as structural Verilog: 4 circuits, main circuit SimplificacaoA
module SimplificacaoA (
  input  [3:0] in_1,
  output out_2
);

  wire not_1_out;

  not not_1 (not_1_out, in_1[3]);
  and and_1 (out_2, in_1[1], not_1_out);
endmodule

module SimplificacaoB (
  input  [3:0] in_1,
  output out_2
);

  wire not_1_out;

  not not_1 (not_1_out, in_1[2]);
  and and_1 (out_2, in_1[1], not_1_out, in_1[3]);
endmodule

module SimplificacaoC (
  input  [3:0] in_1,
  output out_2
);

  wire not_1_out;

  not not_1 (not_1_out, in_1[0]);
  and and_1 (out_2, not_1_out, in_1[2], in_1[3]);
endmodule

module main (
  input  [3:0] a_b_c_d,
  output resp
);

  wire simplificacaoa_1_out_2, simplificacaob_1_out_2, simplificacaoc_1_out_2;

  SimplificacaoA simplificacaoa_1 (.in_1(a_b_c_d), .out_2(simplificacaoa_1_out_2));
  SimplificacaoB simplificacaob_1 (.in_1(a_b_c_d), .out_2(simplificacaob_1_out_2));
  SimplificacaoC simplificacaoc_1 (.in_1(a_b_c_d), .out_2(simplificacaoc_1_out_2));
  or or_1 (resp, simplificacaoa_1_out_2, simplificacaob_1_out_2, simplificacaoc_1_out_2);

  // Notes on the sheet:
  //                  Pedro Siqueira - 405830
endmodule
