// Logisim project Exercicio02.circ as structural Verilog: 6 circuits, main circuit SimpliA
module SimpliA (
  input  [3:0] in_1,
  output out_2
);

  wire not_1_out, not_2_out, not_3_out;

  not not_1 (not_1_out, in_1[0]);
  not not_2 (not_2_out, in_1[2]);
  not not_3 (not_3_out, in_1[3]);
  and and_1 (out_2, not_1_out, not_2_out, not_3_out);
endmodule

module SimpliB (
  input  [3:0] in_1,
  output out_2
);

  wire not_1_out;

  not not_1 (not_1_out, in_1[2]);
  and and_1 (out_2, in_1[0], not_1_out, in_1[3]);
endmodule

module SimpliC (
  input  [3:0] in_1,
  output out_2
);

  wire not_1_out, not_2_out, not_3_out;

  not not_1 (not_1_out, in_1[0]);
  not not_2 (not_2_out, in_1[1]);
  not not_3 (not_3_out, in_1[3]);
  and and_1 (out_2, not_1_out, not_2_out, not_3_out);
endmodule

module SimpliD (
  input  [3:0] in_1,
  output out_2
);

  wire not_1_out, not_2_out;

  not not_1 (not_1_out, in_1[1]);
  not not_2 (not_2_out, in_1[2]);
  and and_1 (out_2, not_1_out, not_2_out, in_1[3]);
endmodule

module SimpliE (
  input  [3:0] in_1,
  output out_2
);

  wire not_1_out;

  not not_1 (not_1_out, in_1[1]);
  and and_1 (out_2, in_1[0], not_1_out, in_1[3]);
endmodule

module main (
  input  [3:0] in_1,
  output out_2
);

  wire simplia_1_out_2, simplib_1_out_2, simplic_1_out_2, simplid_1_out_2, simplie_1_out_2;

  SimpliA simplia_1 (.in_1(in_1), .out_2(simplia_1_out_2));
  SimpliB simplib_1 (.in_1(in_1), .out_2(simplib_1_out_2));
  SimpliC simplic_1 (.in_1(in_1), .out_2(simplic_1_out_2));
  SimpliD simplid_1 (.in_1(in_1), .out_2(simplid_1_out_2));
  SimpliE simplie_1 (.in_1(in_1), .out_2(simplie_1_out_2));
  or or_1 (out_2, simplia_1_out_2, simplib_1_out_2, simplic_1_out_2, simplid_1_out_2, simplie_1_out_2);

  // Notes on the sheet:
  //                      Pedro Siqueria 405830
endmodule
