// Logisim project Exercicio03.circ as structural Verilog: 12 circuits, main circuit SimpliA
module SimpliA (
  input  [4:0] in_1,
  output out_2
);

  wire not_1_out, not_2_out, not_3_out;

  not not_1 (not_1_out, in_1[1]);
  not not_2 (not_2_out, in_1[3]);
  not not_3 (not_3_out, in_1[4]);
  and and_1 (out_2, not_1_out, not_2_out, not_3_out);
endmodule

module SimpliB (
  input  [4:0] in_1,
  output out_2
);

  wire not_1_out, not_2_out, not_3_out;

  not not_1 (not_1_out, in_1[1]);
  not not_2 (not_2_out, in_1[3]);
  not not_3 (not_3_out, in_1[4]);
  and and_1 (out_2, not_1_out, in_1[2], not_2_out, not_3_out);
endmodule

module SimpliC (
  input  [4:0] in_1,
  output out_2
);

  wire not_1_out;

  and and_1 (out_2, in_1[0], in_1[1], in_1[2], not_1_out);
  not not_1 (not_1_out, in_1[4]);
endmodule

module SimpliD (
  input  [4:0] in_1,
  output out_2
);

  wire not_1_out, not_2_out;

  not not_1 (not_1_out, in_1[1]);
  and and_1 (out_2, in_1[0], not_1_out, in_1[3], not_2_out);
  not not_2 (not_2_out, in_1[4]);
endmodule

module SimpliE (
  input  [4:0] in_1,
  output out_2
);

  and and_1 (out_2, in_1[1], in_1[2], in_1[3]);
endmodule

module SimpliF (
  input  [4:0] in_1,
  output out_2
);

  wire not_1_out, not_2_out;

  not not_1 (not_1_out, in_1[1]);
  and and_1 (out_2, not_1_out, in_1[2], not_2_out, in_1[4]);
  not not_2 (not_2_out, in_1[3]);
endmodule

module SimpliG (
  input  [4:0] in_1,
  output out_2
);

  and and_1 (out_2, in_1[0], in_1[1], in_1[2], in_1[4]);
endmodule

module SimpliH (
  input  [4:0] in_1,
  output out_2
);

  and and_1 (out_2, in_1[0], in_1[1], in_1[3], in_1[4]);
endmodule

module SimpliI (
  input  [4:0] in_1,
  output out_2
);

  and and_1 (out_2, in_1[0], in_1[2], in_1[3], in_1[4]);
endmodule

module SimpliJ (
  input  [4:0] in_1,
  output out_2
);

  wire not_1_out, not_2_out, not_3_out;

  not not_1 (not_1_out, in_1[1]);
  not not_2 (not_2_out, in_1[2]);
  not not_3 (not_3_out, in_1[3]);
  and and_1 (out_2, in_1[0], not_1_out, not_2_out, not_3_out, in_1[4]);
endmodule

module SimpleK (
  input  [4:0] in_1,
  output out_2
);

  wire not_1_out, not_2_out, not_3_out;

  not not_1 (not_1_out, in_1[0]);
  not not_2 (not_2_out, in_1[2]);
  not not_3 (not_3_out, in_1[3]);
  and and_1 (out_2, not_1_out, in_1[1], not_2_out, not_3_out, in_1[4]);
endmodule

module main (
  input  [4:0] in_1,
  output out_2
);

  wire or_1_out, or_2_out, simplek_1_out_2, simplia_1_out_2, simplib_1_out_2, simplic_1_out_2,
       simplid_1_out_2, simplie_1_out_2, simplif_1_out_2, simplig_1_out_2, simplih_1_out_2, simplii_1_out_2,
       simplij_1_out_2;

  SimpliA simplia_1 (.in_1(in_1), .out_2(simplia_1_out_2));
  SimpliB simplib_1 (.in_1(in_1), .out_2(simplib_1_out_2));
  SimpliC simplic_1 (.in_1(in_1), .out_2(simplic_1_out_2));
  SimpliD simplid_1 (.in_1(in_1), .out_2(simplid_1_out_2));
  SimpliE simplie_1 (.in_1(in_1), .out_2(simplie_1_out_2));
  SimpliF simplif_1 (.in_1(in_1), .out_2(simplif_1_out_2));
  SimpliG simplig_1 (.in_1(in_1), .out_2(simplig_1_out_2));
  SimpliH simplih_1 (.in_1(in_1), .out_2(simplih_1_out_2));
  SimpliI simplii_1 (.in_1(in_1), .out_2(simplii_1_out_2));
  SimpliJ simplij_1 (.in_1(in_1), .out_2(simplij_1_out_2));
  SimpleK simplek_1 (.in_1(in_1), .out_2(simplek_1_out_2));
  or or_1 (or_1_out, simplia_1_out_2, simplib_1_out_2, simplic_1_out_2, simplid_1_out_2, simplie_1_out_2);
  or or_2 (or_2_out, simplif_1_out_2, simplig_1_out_2, simplih_1_out_2, simplii_1_out_2, simplij_1_out_2, simplek_1_out_2);
  or or_3 (out_2, or_1_out, or_2_out);

  // Notes on the sheet:
  //   Pedro Sqiueria
  //   405830
endmodule
