// Logisim project exercicio02.circ as structural Verilog: 1 circuit, main circuit main
module main (
  input  a,
  input  b,
  input  c,
  input  d,
  output s
);

  wire and_1_out, and_2_out, and_3_out, and_4_out, and_5_out, not_1_out, not_2_out, not_3_out, not_4_out;

  not not_1 (not_1_out, a);
  not not_2 (not_2_out, b);
  not not_3 (not_3_out, c);
  not not_4 (not_4_out, d);
  and and_1 (and_1_out, not_1_out, not_2_out, not_4_out);
  and and_2 (and_2_out, not_1_out, not_3_out, not_4_out);
  and and_3 (and_3_out, a, not_3_out, not_2_out);
  and and_4 (and_4_out, a, not_3_out, d);
  and and_5 (and_5_out, a, not_2_out, d);
  or or_1 (s, and_1_out, and_2_out, and_3_out, and_4_out, and_5_out);

  // Notes on the sheet:
  //   Arquitetura de Computadores - Guia 08
  //   Exercicio 02 - Fazer a saida para a fun玢o
  //   琣琤琩 + 琣琧琩 + 琣琤琧 + a琧d + a琤c
  //   Tiago Menegaz de Melo Garcia        405844
endmodule
