// Logisim project exercicio04.circ as structural Verilog: 4 circuits, main circuit main
module main (
  input  a,
  input  b,
  input  c,
  input  d,
  output s
);

  wire nandand_1_out_3, nandand_2_out_3, nandand_3_out_3, nandand_4_out_3, nandand_5_out_3, nandand_6_out_3,
       nandand_7_out_3, nandnot_1_out_2, nandnot_2_out_2;

  nandnot nandnot_1 (.in_1(b), .out_2(nandnot_1_out_2));
  nandnot nandnot_2 (.in_1(d), .out_2(nandnot_2_out_2));
  nandand nandand_1 (.in_1(nandnot_2_out_2), .in_2(c), .out_3(nandand_1_out_3));
  nandand nandand_2 (.in_2(a), .out_3(nandand_2_out_3));  // open: in_1
  nandand nandand_3 (.in_1(nandnot_2_out_2), .in_2(b), .out_3(nandand_3_out_3));
  nandand nandand_4 (.in_1(c), .out_3(nandand_4_out_3));  // open: in_2
  nandand nandand_5 (.in_1(nandnot_1_out_2), .in_2(a), .out_3(nandand_5_out_3));
  nandand nandand_6 (.in_1(nandand_2_out_3), .in_2(nandand_3_out_3), .out_3(nandand_6_out_3));
  nandand nandand_7 (.in_1(nandand_4_out_3), .in_2(nandand_5_out_3), .out_3(nandand_7_out_3));
  nandor nandor_1 (.in_1(nandand_1_out_3), .in_2(nandand_6_out_3), .in_3(nandand_7_out_3), .out_4(s));

  // Notes on the sheet:
  //   Arquitetura de Computadores - Guia 08
  //   Exercicio 04 - Refazer o Exercicio 01 com portas NAND
  //   ¬ac + ab¬d + a¬bc
  //   Tiago Menegaz de Melo Garcia        405844
endmodule

module nandand (
  input  in_1,
  input  in_2,
  output out_3
);

  wire nand_1_out;

  nand nand_1 (nand_1_out, in_1, in_2);
  not nand_2 (out_3, nand_1_out);  // NAND_Gate
endmodule

module nandnot (
  input  in_1,
  output out_2
);

  not nand_1 (out_2, in_1);  // NAND_Gate
endmodule

module nandor (
  input  in_1,
  input  in_2,
  input  in_3,
  output out_4
);

  wire nand_1_out, nand_2_out, nand_3_out;

  not nand_1 (nand_1_out, in_1);  // NAND_Gate
  not nand_2 (nand_2_out, in_2);  // NAND_Gate
  not nand_3 (nand_3_out, in_3);  // NAND_Gate
  nand nand_4 (out_4, nand_1_out, nand_2_out, nand_3_out);
endmodule
