// Logisim project exercicio05.circ as structural Verilog: 3 circuits, main circuit main
module main (
  input  a,
  input  b,
  input  c,
  input  d,
  output out_5
);

  wire andnor_1_out_4, andnor_2_out_4, andnor_3_out_4, andnor_4_out_4, nor_1_out, notnor_1_out_2,
       notnor_2_out_2, notnor_3_out_2, notnor_4_out_2;

  notnor notnor_1 (.in_1(a), .out_2(notnor_1_out_2));
  notnor notnor_2 (.in_1(b), .out_2(notnor_2_out_2));
  notnor notnor_3 (.in_1(c), .out_2(notnor_3_out_2));
  notnor notnor_4 (.in_1(d), .out_2(notnor_4_out_2));
  andnor andnor_1 (.in_1(notnor_1_out_2), .in_2(notnor_2_out_2), .in_3(notnor_4_out_2), .out_4(andnor_1_out_4));
  andnor andnor_2 (.in_1(notnor_1_out_2), .in_2(notnor_3_out_2), .in_3(notnor_4_out_2), .out_4(andnor_2_out_4));
  andnor andnor_3 (.in_1(a), .in_2(notnor_3_out_2), .in_3(d), .out_4(andnor_3_out_4));
  andnor andnor_4 (.in_1(a), .in_2(notnor_2_out_2), .in_3(d), .out_4(andnor_4_out_4));
  nor nor_1 (nor_1_out, andnor_1_out_4, andnor_2_out_4, andnor_3_out_4, andnor_4_out_4);
  not nor_2 (out_5, nor_1_out);  // NOR_Gate

  // Notes on the sheet:
  //   Arquitetura de Computadores - Guia 08
  //   Exercicio 05 - Refazer o Exercicio 02 com portas NOR
  //   ¬(abd) + ¬(acd) + ¬(abc) + a¬cd + a¬bc
  //   Tiago Menegaz de Melo Garcia        405844
endmodule

module notnor (
  input  in_1,
  output out_2
);

  not nor_1 (out_2, in_1);  // NOR_Gate
endmodule

module andnor (
  input  in_1,
  input  in_2,
  input  in_3,
  output out_4
);

  wire nor_1_out, nor_2_out, nor_3_out;

  not nor_1 (nor_1_out, in_1);  // NOR_Gate
  not nor_2 (nor_2_out, in_2);  // NOR_Gate
  not nor_3 (nor_3_out, in_3);  // NOR_Gate
  nor nor_4 (out_4, nor_1_out, nor_2_out, nor_3_out);
endmodule
