// Logisim project exercicio01.circ as structural Verilog: 1 circuit, main circuit main
module main (
  input  a,
  input  b,
  input  c,
  input  d,
  output s
);

  wire and_1_out, and_2_out, and_3_out, not_1_out, not_2_out, not_3_out;

  not not_1 (not_1_out, a);
  not not_2 (not_2_out, b);
  not not_3 (not_3_out, d);
  and and_1 (and_1_out, not_1_out, c);
  and and_2 (and_2_out, not_2_out, c);
  and and_3 (and_3_out, not_3_out, b, a);
  or or_1 (s, and_1_out, and_2_out, and_3_out);

  // Notes on the sheet:
  //   Matrícula: 407450
  //   Nome: Jéssica Daniela
  //   Exercicio 01
endmodule
