// Logisim project exercicio03.circ as structural Verilog: 1 circuit, main circuit main
module main (
  input  a,
  input  b,
  input  c,
  input  d,
  input  e,
  output out_6
);

  wire and_1_out, and_2_out, and_3_out, and_4_out, and_5_out, and_6_out, and_7_out, and_8_out, and_9_out,
       not_1_out, not_2_out, not_3_out, not_4_out, not_5_out;

  not not_1 (not_1_out, a);
  not not_2 (not_2_out, b);
  not not_3 (not_3_out, c);
  not not_4 (not_4_out, d);
  not not_5 (not_5_out, e);
  and and_1 (and_1_out, b, c, e);
  and and_2 (and_2_out, b, c, d);
  and and_3 (and_3_out, e, d, c);
  and and_4 (and_4_out, not_4_out, not_2_out, not_1_out);
  and and_5 (and_5_out, not_4_out, not_3_out, b, not_1_out);
  and and_6 (and_6_out, not_4_out, c, not_2_out, a);
  and and_7 (and_7_out, e, d, b, a);
  and and_8 (and_8_out, d, not_4_out, not_3_out, not_2_out, a);
  and and_9 (and_9_out, d, not_5_out, not_3_out, not_2_out, a);
  or or_1 (out_6, and_1_out, and_2_out, and_3_out, and_4_out, and_5_out, and_6_out, and_7_out, and_8_out, and_9_out);

  // Notes on the sheet:
  //   Matrícula: 407450
  //   Nome: Jéssica Daniela
  //   Exercicio 03
endmodule
