// Logisim project exercicio04.circ as structural Verilog: 1 circuit, main circuit main
module main (
  input  A,
  input  B,
  input  C,
  input  D,
  output S
);

  wire nand_1_out, nand_2_out, nand_3_out, nand_4_out, nand_5_out, nand_6_out;

  not nand_1 (nand_1_out, A);  // NAND_Gate
  not nand_2 (nand_2_out, B);  // NAND_Gate
  not nand_3 (nand_3_out, D);  // NAND_Gate
  nand nand_4 (nand_4_out, nand_1_out, C);
  not nand_5 (nand_5_out, nand_2_out);  // NAND_Gate
  nand nand_6 (nand_6_out, A, B, nand_3_out);
  nand nand_7 (S, nand_4_out, nand_5_out, nand_6_out);

  // Notes on the sheet:
  //   Nome: Jéssica Daniela
  //   Matricula: 407450
  //   Exercicio 04
endmodule
