// Logisim project Exercicio01.circ as structural Verilog: 1 circuit, main circuit main
module main (
  input  [3:0] a_b_c_d,
  output s0
);

  wire and_1_out, and_2_out, and_3_out, not_1_out, not_2_out, not_3_out;

  not not_1 (not_1_out, a_b_c_d[0]);
  not not_2 (not_2_out, a_b_c_d[2]);
  not not_3 (not_3_out, a_b_c_d[3]);
  and and_1 (and_1_out, not_1_out, a_b_c_d[2], a_b_c_d[3]);
  and and_2 (and_2_out, a_b_c_d[1], not_2_out, a_b_c_d[3]);
  and and_3 (and_3_out, not_3_out, a_b_c_d[1]);
  or or_1 (s0, and_1_out, and_2_out, and_3_out);
endmodule
