// Logisim project Exercicio03.circ as structural Verilog: 1 circuit, main circuit main
module main (
  input  [4:0] a_b_c_d_e,
  output s0
);

  wire and_1_out, and_2_out, and_3_out, and_4_out, and_5_out, and_6_out, and_7_out, and_8_out, not_2_out,
       not_3_out, not_4_out, not_5_out, not_6_out, not_7_out, not_8_out, not_9_out, not_10_out, not_11_out,
       not_12_out, not_13_out, not_14_out, not_15_out;

  // NOT_Gate not_1 is placed but not wired
  not not_2 (not_2_out, a_b_c_d_e[4]);
  not not_3 (not_3_out, a_b_c_d_e[2]);
  not not_4 (not_4_out, a_b_c_d_e[1]);
  not not_5 (not_5_out, a_b_c_d_e[1]);
  not not_6 (not_6_out, a_b_c_d_e[3]);
  not not_7 (not_7_out, a_b_c_d_e[1]);
  not not_8 (not_8_out, a_b_c_d_e[0]);
  not not_9 (not_9_out, a_b_c_d_e[3]);
  not not_10 (not_10_out, a_b_c_d_e[3]);
  not not_11 (not_11_out, a_b_c_d_e[2]);
  not not_12 (not_12_out, a_b_c_d_e[1]);
  not not_13 (not_13_out, a_b_c_d_e[3]);
  not not_14 (not_14_out, a_b_c_d_e[2]);
  not not_15 (not_15_out, a_b_c_d_e[0]);
  and and_1 (and_1_out, a_b_c_d_e[4], a_b_c_d_e[3], a_b_c_d_e[1], a_b_c_d_e[0]);
  and and_2 (and_2_out, a_b_c_d_e[3], a_b_c_d_e[2], a_b_c_d_e[1]);
  and and_3 (and_3_out, not_2_out, not_3_out, not_4_out);
  and and_4 (and_4_out, a_b_c_d_e[2], not_5_out, a_b_c_d_e[0]);
  and and_5 (and_5_out, not_6_out, a_b_c_d_e[2], not_7_out, not_8_out);
  and and_6 (and_6_out, not_9_out, a_b_c_d_e[2], a_b_c_d_e[1], a_b_c_d_e[0]);
  and and_7 (and_7_out, not_10_out, not_11_out, not_12_out, a_b_c_d_e[0]);
  and and_8 (and_8_out, a_b_c_d_e[4], not_13_out, not_14_out, a_b_c_d_e[1], not_15_out);
  or or_1 (s0, and_1_out, and_2_out, and_3_out, and_4_out, and_5_out, and_6_out, and_7_out, and_8_out);
endmodule
