// Logisim project guia 8 - 412727.circ as structural Verilog: 8 circuits, main circuit main
module main (
  input  a,
  input  b,
  input  c,
  input  d,
  input  e,
  output Exercicio_1,
  output Exercicio_2,
  output Exercicio_3,
  output out_9,
  output out_10,
  output out_11,
  output out_12
);

  Exercicio_1 exercicio_1_1 (.a(a), .b(b), .c(c), .d(d), .s(Exercicio_1));
  Exercicio_2 exercicio_2_1 (.a(a), .b(b), .c(c), .d(d), .out_5(Exercicio_2));
  Exercicio_3 exercicio_3_1 (.A(a), .B(b), .C(c), .D(d), .E(e), .S(Exercicio_3));
  exercicio_1__nand___extra exercicio_1_nand_extra_1 (.a(a), .b(b), .c(c), .d(d), .s(out_9));
  exercicio_1__nor___extra exercicio_1_nor_extra_1 (.a(a), .b(b), .c(c), .d(d), .s(out_10));
  exercicio_2__nand__extra exercicio_2_nand_extra_1 (.a(a), .b(b), .c(c), .d(d), .out_5(out_11));
  exercicio_2__nor__extra exercicio_2_nor_extra_1 (.a(a), .b(b), .c(c), .d(d), .out_5(out_12));

  // Notes on the sheet:
  //   412727
  //   Augusto Ferreira Andrade do Carmo
  //   exercicio 1 (nand)(extra)
  //   exercicio 1 (nor)(extra)
  //   exercicio 2 (nand)(extra)
  //   exercicio 2 (nor)(extra)
  //   nos exercicios 1 e 2, a = 2^3; b= 2^2; c= 2^1; d = 2^0
  //   no exercicio 3, a =2^4; b = 2^3; c = 2^2; d = 2^1 ; e = 2 ^0
endmodule

module Exercicio_1 (
  input  a,
  input  b,
  input  c,
  input  d,
  output s
);

  wire and_1_out, and_2_out, and_3_out, and_4_out, not_1_out, not_2_out, not_3_out, not_4_out;

  and and_1 (and_1_out, a, b, not_1_out);
  not not_1 (not_1_out, d);
  and and_2 (and_2_out, c, not_2_out);
  not not_2 (not_2_out, d);
  and and_3 (and_3_out, c, not_3_out);
  not not_3 (not_3_out, b);
  not not_4 (not_4_out, a);
  and and_4 (and_4_out, not_4_out, c);
  or or_1 (s, and_2_out, and_1_out, and_4_out, and_3_out);
endmodule

module Exercicio_2 (
  input  a,
  input  b,
  input  c,
  input  d,
  output out_5
);

  wire nand_1_out, nand_2_out, nand_3_out, nand_4_out, nand_5_out, nand_6_out, nand_7_out, nand_8_out,
       nand_9_out, nand_10_out, nand_11_out, nand_12_out, nand_13_out, nand_14_out, nand_15_out, nand_16_out;

  not nand_1 (nand_1_out, a);  // NAND_Gate
  not nand_2 (nand_2_out, d);  // NAND_Gate
  not nand_3 (nand_3_out, a);  // NAND_Gate
  not nand_4 (nand_4_out, d);  // NAND_Gate
  not nand_5 (nand_5_out, b);  // NAND_Gate
  not nand_6 (nand_6_out, d);  // NAND_Gate
  not nand_7 (nand_7_out, b);  // NAND_Gate
  not nand_8 (nand_8_out, c);  // NAND_Gate
  not nand_9 (nand_9_out, b);  // NAND_Gate
  not nand_10 (nand_10_out, c);  // NAND_Gate
  not nand_11 (nand_11_out, c);  // NAND_Gate
  nand nand_12 (nand_12_out, nand_1_out, nand_9_out, nand_2_out);
  nand nand_13 (nand_13_out, nand_3_out, nand_10_out, nand_4_out);
  nand nand_14 (nand_14_out, nand_5_out, nand_11_out, nand_6_out);
  nand nand_15 (nand_15_out, a, nand_7_out, d);
  nand nand_16 (nand_16_out, a, nand_8_out, d);
  nand nand_17 (out_5, nand_12_out, nand_13_out, nand_14_out, nand_15_out, nand_16_out);
endmodule

module Exercicio_3 (
  input  A,
  input  B,
  input  C,
  input  D,
  input  E,
  output S
);

  wire and_1_out, and_2_out, and_3_out, and_4_out, and_5_out, and_6_out, and_7_out, and_8_out, and_9_out,
       not_1_out, not_2_out, not_3_out, not_4_out, not_5_out, not_6_out, not_7_out, not_8_out, not_9_out,
       not_10_out, not_11_out, not_12_out, not_13_out, not_14_out, not_15_out;

  not not_1 (not_1_out, B);
  not not_2 (not_2_out, C);
  not not_3 (not_3_out, E);
  not not_4 (not_4_out, A);
  not not_5 (not_5_out, C);
  not not_6 (not_6_out, D);
  not not_7 (not_7_out, B);
  not not_8 (not_8_out, D);
  not not_9 (not_9_out, B);
  not not_10 (not_10_out, D);
  not not_11 (not_11_out, A);
  not not_12 (not_12_out, D);
  not not_13 (not_13_out, A);
  not not_14 (not_14_out, B);
  not not_15 (not_15_out, D);
  and and_1 (and_1_out, A, not_1_out, not_2_out, D, not_3_out);
  and and_2 (and_2_out, A, B, D, E);
  and and_3 (and_3_out, not_4_out, B, not_5_out, not_6_out);
  and and_4 (and_4_out, not_7_out, not_8_out, E);
  and and_5 (and_5_out, not_9_out, C, not_10_out);
  and and_6 (and_6_out, B, C, D);
  and and_7 (and_7_out, not_11_out, not_12_out, E);
  and and_8 (and_8_out, not_13_out, not_14_out, not_15_out);
  and and_9 (and_9_out, C, E);
  or or_1 (S, and_1_out, and_2_out, and_3_out, and_4_out, and_5_out, and_6_out, and_7_out, and_8_out, and_9_out);

  // Notes on the sheet:
  //   A
  //   B
  //   E
  //   F
  //   G
  //   H
  //   I
  //   J
  //   K
endmodule

module exercicio_1__nand___extra (
  input  a,
  input  b,
  input  c,
  input  d,
  output s
);

  wire nand_1_out, nand_2_out, nand_3_out, nand_4_out, nand_5_out, nand_6_out, nand_7_out, nand_8_out;

  not nand_1 (nand_1_out, d);  // NAND_Gate
  not nand_2 (nand_2_out, d);  // NAND_Gate
  not nand_3 (nand_3_out, b);  // NAND_Gate
  not nand_4 (nand_4_out, a);  // NAND_Gate
  nand nand_5 (nand_5_out, a, b, nand_1_out);
  nand nand_6 (nand_6_out, c, nand_2_out);
  nand nand_7 (nand_7_out, c, nand_3_out);
  nand nand_8 (nand_8_out, nand_4_out, c);
  nand nand_9 (s, nand_5_out, nand_6_out, nand_7_out, nand_8_out);
endmodule

module exercicio_1__nor___extra (
  input  a,
  input  b,
  input  c,
  input  d,
  output s
);

  wire nor_1_out, nor_2_out, nor_3_out, nor_4_out, nor_5_out, nor_6_out, nor_7_out, nor_8_out, nor_9_out,
       nor_10_out;

  not nor_1 (nor_1_out, a);  // NOR_Gate
  not nor_2 (nor_2_out, c);  // NOR_Gate
  not nor_3 (nor_3_out, c);  // NOR_Gate
  not nor_4 (nor_4_out, c);  // NOR_Gate
  not nor_5 (nor_5_out, b);  // NOR_Gate
  nor nor_6 (nor_6_out, nor_1_out, nor_5_out, d);
  nor nor_7 (nor_7_out, nor_2_out, d);
  nor nor_8 (nor_8_out, nor_3_out, b);
  nor nor_9 (nor_9_out, a, nor_4_out);
  nor nor_10 (nor_10_out, nor_7_out, nor_6_out, nor_9_out, nor_8_out);
  not nor_11 (s, nor_10_out);  // NOR_Gate
endmodule

module exercicio_2__nand__extra (
  input  a,
  input  b,
  input  c,
  input  d,
  output out_5
);

  wire nand_1_out, nand_2_out, nand_3_out, nand_4_out, nand_5_out, nand_6_out, nand_7_out, nand_8_out,
       nand_9_out, nand_10_out, nand_11_out, nand_12_out, nand_13_out, nand_14_out, nand_15_out, nand_16_out;

  not nand_1 (nand_1_out, a);  // NAND_Gate
  not nand_2 (nand_2_out, d);  // NAND_Gate
  not nand_3 (nand_3_out, a);  // NAND_Gate
  not nand_4 (nand_4_out, d);  // NAND_Gate
  not nand_5 (nand_5_out, b);  // NAND_Gate
  not nand_6 (nand_6_out, d);  // NAND_Gate
  not nand_7 (nand_7_out, b);  // NAND_Gate
  not nand_8 (nand_8_out, c);  // NAND_Gate
  not nand_9 (nand_9_out, b);  // NAND_Gate
  not nand_10 (nand_10_out, c);  // NAND_Gate
  not nand_11 (nand_11_out, c);  // NAND_Gate
  nand nand_12 (nand_12_out, nand_1_out, nand_9_out, nand_2_out);
  nand nand_13 (nand_13_out, nand_3_out, nand_10_out, nand_4_out);
  nand nand_14 (nand_14_out, nand_5_out, nand_11_out, nand_6_out);
  nand nand_15 (nand_15_out, a, nand_7_out, d);
  nand nand_16 (nand_16_out, a, nand_8_out, d);
  nand nand_17 (out_5, nand_12_out, nand_13_out, nand_14_out, nand_15_out, nand_16_out);
endmodule

module exercicio_2__nor__extra (
  input  a,
  input  b,
  input  c,
  input  d,
  output out_5
);

  wire nor_1_out, nor_2_out, nor_3_out, nor_4_out, nor_5_out, nor_6_out, nor_7_out, nor_8_out, nor_9_out,
       nor_10_out;

  not nor_1 (nor_1_out, a);  // NOR_Gate
  not nor_2 (nor_2_out, d);  // NOR_Gate
  not nor_3 (nor_3_out, a);  // NOR_Gate
  not nor_4 (nor_4_out, d);  // NOR_Gate
  nor nor_5 (nor_5_out, a, b, d);
  nor nor_6 (nor_6_out, a, c, d);
  nor nor_7 (nor_7_out, b, c, d);
  nor nor_8 (nor_8_out, nor_1_out, b, nor_2_out);
  nor nor_9 (nor_9_out, nor_3_out, c, nor_4_out);
  nor nor_10 (nor_10_out, nor_5_out, nor_6_out, nor_7_out, nor_8_out, nor_9_out);
  not nor_11 (out_5, nor_10_out);  // NOR_Gate
endmodule
