// Logisim project Circuitos.circ as structural Verilog: 4 circuits, main circuit Exercicio1
module Exercicio1 (
  input  a,
  input  b,
  input  c,
  input  d,
  output s0
);

  wire and_1_out, and_2_out, and_3_out, not_1_out, not_2_out, not_3_out;

  not not_1 (not_1_out, d);
  not not_2 (not_2_out, b);
  not not_3 (not_3_out, a);
  and and_1 (and_1_out, a, b, not_1_out);
  and and_2 (and_2_out, not_2_out, c);
  and and_3 (and_3_out, not_3_out, c);
  or or_1 (s0, and_1_out, and_2_out, and_3_out);

  // Notes on the sheet:
  //   Fabrício Rodrigues de Souza - 412737
  //   Guia 08
endmodule

module Exercicio2 (
  input  a,
  input  b,
  input  c,
  input  d,
  output S1
);

  wire and_1_out, and_2_out, and_3_out, and_4_out, and_5_out, not_1_out, not_2_out, not_3_out, not_4_out,
       not_5_out, not_6_out, not_7_out, not_8_out, not_9_out, not_10_out, not_11_out;

  not not_1 (not_1_out, a);
  not not_2 (not_2_out, b);
  not not_3 (not_3_out, d);
  not not_4 (not_4_out, a);
  not not_5 (not_5_out, c);
  not not_6 (not_6_out, d);
  not not_7 (not_7_out, b);
  not not_8 (not_8_out, c);
  not not_9 (not_9_out, d);
  not not_10 (not_10_out, b);
  not not_11 (not_11_out, c);
  and and_1 (and_1_out, not_1_out, not_2_out, not_3_out);
  and and_2 (and_2_out, not_4_out, not_5_out, not_6_out);
  and and_3 (and_3_out, not_7_out, not_8_out, not_9_out);
  and and_4 (and_4_out, a, not_10_out, d);
  and and_5 (and_5_out, a, not_11_out, d);
  or or_1 (S1, and_1_out, and_2_out, and_3_out, and_4_out, and_5_out);

  // Notes on the sheet:
  //   Fabrício Rodrigues de Souza - 412737
  //   Guia 08
endmodule

module Exercicio3 (
  input  a,
  input  b,
  input  c,
  input  d,
  input  e,
  output S0
);

  wire and_1_out, and_2_out, and_3_out, and_4_out, and_5_out, and_6_out, and_7_out, and_8_out, not_1_out,
       not_2_out, not_3_out, not_4_out, not_5_out;

  not not_1 (not_1_out, a);
  not not_2 (not_2_out, b);
  not not_3 (not_3_out, c);
  not not_4 (not_4_out, d);
  not not_5 (not_5_out, e);
  and and_1 (and_1_out, a, not_2_out, not_3_out, d, e);
  and and_2 (and_2_out, a, b, d, e);
  and and_3 (and_3_out, not_1_out, not_3_out, not_4_out);
  and and_4 (and_4_out, not_2_out, not_4_out, not_5_out);
  and and_5 (and_5_out, not_2_out, c, not_4_out);
  and and_6 (and_6_out, c, d, e);
  and and_7 (and_7_out, b, c, e);
  and and_8 (and_8_out, b, c, d);
  or or_1 (S0, and_1_out, and_2_out, and_3_out, and_4_out, and_5_out, and_6_out, and_7_out, and_8_out);

  // Notes on the sheet:
  //   Fabrício Rodrigues de Souza - 412737
  //   Guia 08
endmodule

module Main (
  input  a,
  input  b,
  input  c,
  input  d,
  input  e,
  output S_1__Saida_Exercicio01,
  output S_2__Saida_Exercicio02,
  output S_3___Saida_Exercicio03
);

  Exercicio1 exercicio1_1 (.a(a), .b(b), .c(c), .d(d), .s0(S_1__Saida_Exercicio01));
  Exercicio2 exercicio2_1 (.a(a), .b(b), .c(c), .d(d), .S1(S_2__Saida_Exercicio02));
  Exercicio3 exercicio3_1 (.a(a), .b(b), .c(c), .d(d), .e(e), .S0(S_3___Saida_Exercicio03));

  // Notes on the sheet:
  //   Fabrício Rodrigues de Souza - 412737
  //   Guia 08
endmodule
