// Logisim project Guia0802.circ as structural Verilog: 1 circuit, main circuit main
module main (
  input  [3:0] a,
  output s
);

  wire and_1_out, and_2_out, and_3_out, and_4_out, and_5_out, not_1_out, not_2_out, not_3_out, not_4_out;

  not not_1 (not_1_out, a[0]);
  not not_2 (not_2_out, a[1]);
  not not_3 (not_3_out, a[2]);
  not not_4 (not_4_out, a[3]);
  and and_1 (and_1_out, not_3_out, not_1_out, not_4_out);
  and and_2 (and_2_out, not_1_out, not_2_out, not_4_out);
  and and_3 (and_3_out, not_2_out, not_3_out, a[3]);
  and and_4 (and_4_out, a[0], not_3_out, a[3]);
  and and_5 (and_5_out, not_2_out, a[0], a[3]);
  or or_1 (s, and_1_out, and_2_out, and_3_out, and_4_out, and_5_out);

  // Notes on the sheet:
  //   Lucas Teixeira Santos - Guia 08 Ex02
  //   Simplificacao (Vide Verilog):
  //   (~a3.~a2.~a0) + (~a3.~a1.~a0) + (a3.~a2.~a1) + (a3.~a2.a0) + (a3.~a1.a0)
endmodule
