// Logisim project Guia0803.circ as structural Verilog: 2 circuits, main circuit main
module main (
  input  [4:0] a,
  output s
);

  wire and4_1_s, and4_2_s, and4_3_s, and4_4_s, and4_5_s, and4_6_s, and4_7_s, and4_8_s, and_1_out, and_2_out,
       not_1_out, not_2_out, not_3_out, not_4_out, not_5_out, or_1_out, or_2_out;

  not not_1 (not_1_out, a[0]);
  not not_2 (not_2_out, a[1]);
  not not_3 (not_3_out, a[2]);
  not not_4 (not_4_out, a[3]);
  not not_5 (not_5_out, a[4]);
  and4 and4_1 (.a(a[1]), .b(a[2]), .c(a[4]), .d(a[3]), .s(and4_1_s));
  and4 and4_2 (.a(not_1_out), .b(a[1]), .c(a[3]), .d(a[2]), .s(and4_2_s));
  and4 and4_3 (.a(not_1_out), .b(not_2_out), .c(not_3_out), .d(a[4]), .s(and4_3_s));
  and4 and4_4 (.a(a[0]), .b(not_2_out), .c(a[2]), .d(a[3]), .s(and4_4_s));
  and4 and4_5 (.a(a[0]), .b(a[1]), .c(a[2]), .d(not_5_out), .s(and4_5_s));
  and4 and4_6 (.a(a[0]), .b(not_2_out), .c(not_3_out), .d(not_4_out), .s(and4_6_s));
  and and_1 (and_1_out, not_2_out, not_3_out, not_5_out);
  and and_2 (and_2_out, not_1_out, not_4_out, not_5_out);
  and4 and4_7 (.a(not_1_out), .b(a[2]), .c(a[4]), .d(not_4_out), .s(and4_7_s));
  and4 and4_8 (.a(not_2_out), .b(a[2]), .c(not_4_out), .d(a[4]), .s(and4_8_s));
  or or_1 (or_1_out, and4_1_s, and4_7_s, and4_2_s, and4_3_s, and4_4_s);
  or or_2 (or_2_out, and4_5_s, and4_6_s, and_1_out, and_2_out, and4_8_s);
  or or_3 (s, or_1_out, or_2_out);

  // Notes on the sheet:
  //   Lucas Teixeira Santos - Guia 08 Ex01
  //   Simplificacao (Vide Verilog):
  //   ~a~b~d (A) + ~a~c~d (B) + ~b~c~de (C) + ~acde (D) + bc~de (E) + 
  //   a~cde (F) + bcd~e (G) + a~bc~e (H) + abcd (I) + a~bc~d (J)
  //   A até I 
  //   J
  //   (16) está saindo 1.
endmodule

module and4 (
  input  a,
  input  b,
  input  c,
  input  d,
  output s
);

  wire and_1_out, and_2_out;

  and and_1 (and_1_out, a, b);
  and and_2 (and_2_out, c, d);
  and and_3 (s, and_1_out, and_2_out);
endmodule
