// Logisim project Guia0805.circ as structural Verilog: 2 circuits, main circuit main
module main (
  input  [3:0] a,
  output s
);

  wire and_usando_nor_1_s, and_usando_nor_2_s, and_usando_nor_3_s, and_usando_nor_4_s, and_usando_nor_5_s,
       nor_1_out, nor_2_out, nor_3_out, nor_4_out, nor_6_out;

  not nor_1 (nor_1_out, a[0]);  // NOR_Gate
  not nor_2 (nor_2_out, a[1]);  // NOR_Gate
  not nor_3 (nor_3_out, a[2]);  // NOR_Gate
  AND_usando_NOR and_usando_nor_1 (.a(nor_3_out), .b(nor_4_out), .c(nor_1_out), .s(and_usando_nor_1_s));
  AND_usando_NOR and_usando_nor_2 (.a(nor_1_out), .b(nor_2_out), .c(nor_4_out), .s(and_usando_nor_2_s));
  AND_usando_NOR and_usando_nor_3 (.a(nor_2_out), .b(nor_3_out), .c(a[3]), .s(and_usando_nor_3_s));
  not nor_4 (nor_4_out, a[3]);  // NOR_Gate
  AND_usando_NOR and_usando_nor_4 (.a(a[0]), .b(nor_3_out), .c(a[3]), .s(and_usando_nor_4_s));
  AND_usando_NOR and_usando_nor_5 (.a(nor_2_out), .b(a[0]), .c(a[3]), .s(and_usando_nor_5_s));
  not nor_5 (s, nor_6_out);  // NOR_Gate
  nor nor_6 (nor_6_out, and_usando_nor_1_s, and_usando_nor_2_s, and_usando_nor_3_s, and_usando_nor_4_s, and_usando_nor_5_s);

  // Notes on the sheet:
  //   Lucas Teixeira Santos - Guia 08 Ex05
  //   Simplificacao (Vide Verilog):
  //   (~a3.~a2.~a0) + (~a3.~a1.~a0) + (a3.~a2.~a1) + (a3.~a2.a0) + (a3.~a1.a0)
endmodule

module AND_usando_NOR (
  input  a,
  input  b,
  input  c,
  output s
);

  wire nor_1_out, nor_2_out, nor_3_out;

  not nor_1 (nor_1_out, a);  // NOR_Gate
  not nor_2 (nor_2_out, b);  // NOR_Gate
  not nor_3 (nor_3_out, c);  // NOR_Gate
  nor nor_4 (s, nor_1_out, nor_2_out, nor_3_out);
endmodule
