// Logisim project Exercicio01_Logisim.circ as structural Verilog
module Simplificado (
  input  [3:0] ABCD,
  output S
);

  wire and_1_out, and_2_out, and_3_out, not_1_out, not_2_out, not_3_out;

  not not_1 (not_1_out, ABCD[3]);
  and and_1 (and_1_out, not_1_out, ABCD[1]);
  not not_2 (not_2_out, ABCD[2]);
  and and_2 (and_2_out, not_2_out, ABCD[1]);
  and and_3 (and_3_out, ABCD[3], ABCD[2], not_3_out);
  not not_3 (not_3_out, ABCD[0]);
  or or_1 (S, and_1_out, and_2_out, and_3_out);

  // Notes on the sheet:
  //   Jonathan Felipe Xavier Matricula 415704
endmodule
