// Logisim project Exercicio02_Logisim.circ as structural Verilog
module Simplificado (
  input  [3:0] ABCD,
  output S
);

  wire and_1_out, and_2_out, and_3_out, and_4_out, and_5_out, not_1_out, not_2_out, not_3_out, not_4_out,
       not_5_out, not_6_out, not_7_out, not_8_out, not_9_out, not_10_out;

  not not_1 (not_1_out, ABCD[3]);
  and and_1 (and_1_out, not_1_out, not_2_out, not_3_out);
  not not_2 (not_2_out, ABCD[2]);
  not not_3 (not_3_out, ABCD[0]);
  and and_2 (and_2_out, ABCD[3], not_4_out, not_5_out);
  not not_4 (not_4_out, ABCD[1]);
  not not_5 (not_5_out, ABCD[0]);
  and and_3 (and_3_out, ABCD[3], ABCD[0], not_6_out);
  not not_6 (not_6_out, ABCD[1]);
  not not_7 (not_7_out, ABCD[3]);
  not not_8 (not_8_out, ABCD[1]);
  and and_4 (and_4_out, not_7_out, not_8_out, not_9_out);
  not not_9 (not_9_out, ABCD[0]);
  and and_5 (and_5_out, ABCD[3], ABCD[0], not_10_out);
  not not_10 (not_10_out, ABCD[2]);
  or or_1 (S, and_1_out, and_2_out, and_3_out, and_4_out, and_5_out);

  // Notes on the sheet:
  //   Jonathan Felipe  Matricula 415704
endmodule
