// Logisim project Exercicio03_Logisim.circ as structural Verilog
module Simplificado (
  input  [4:0] ABCDE,
  output S
);

  wire and_1_out, and_2_out, and_3_out, and_4_out, and_5_out, and_6_out, and_7_out, and_8_out, and_9_out,
       not_1_out, not_2_out, not_3_out, not_4_out, not_5_out, not_6_out, not_7_out, not_8_out, not_9_out,
       not_10_out, not_11_out, not_12_out, not_13_out, not_14_out, or_1_out, or_2_out;

  not not_1 (not_1_out, ABCDE[4]);
  not not_2 (not_2_out, ABCDE[3]);
  not not_3 (not_3_out, ABCDE[1]);
  not not_4 (not_4_out, ABCDE[4]);
  not not_5 (not_5_out, ABCDE[2]);
  not not_6 (not_6_out, ABCDE[1]);
  not not_7 (not_7_out, ABCDE[3]);
  not not_8 (not_8_out, ABCDE[1]);
  not not_9 (not_9_out, ABCDE[3]);
  not not_10 (not_10_out, ABCDE[1]);
  not not_11 (not_11_out, ABCDE[2]);
  not not_12 (not_12_out, ABCDE[3]);
  not not_13 (not_13_out, ABCDE[2]);
  not not_14 (not_14_out, ABCDE[0]);
  and and_1 (and_1_out, ABCDE[0], ABCDE[2], ABCDE[3]);
  and and_2 (and_2_out, ABCDE[3], ABCDE[2], ABCDE[1]);
  and and_3 (and_3_out, ABCDE[2], ABCDE[1], ABCDE[0]);
  and and_4 (and_4_out, not_1_out, not_2_out, not_3_out);
  and and_5 (and_5_out, not_4_out, ABCDE[3], not_5_out, not_6_out);
  and and_6 (and_6_out, ABCDE[4], not_7_out, ABCDE[2], not_8_out);
  and and_7 (and_7_out, ABCDE[4], ABCDE[3], ABCDE[1], ABCDE[0]);
  and and_8 (and_8_out, ABCDE[4], not_9_out, not_10_out, not_11_out, ABCDE[0]);
  and and_9 (and_9_out, ABCDE[4], not_12_out, not_13_out, not_14_out, ABCDE[1]);
  or or_1 (or_1_out, and_1_out, and_2_out, and_3_out, and_4_out, and_5_out);
  or or_2 (or_2_out, and_6_out, and_7_out, and_8_out, and_9_out);
  or or_3 (S, or_1_out, or_2_out);

  // Notes on the sheet:
  //   Jonathan Felipe Matricula 415704
endmodule
