// Logisim project Exercicio04_Logisim.circ as structural Verilog: 1 circuit, main circuit main
module main (
  input  [3:0] ABCD,
  output S
);

  wire nand_1_out, nand_2_out, nand_3_out, nand_4_out, nand_5_out, nand_6_out;

  nand nand_1 (nand_1_out, ABCD[3], ABCD[3]);
  nand nand_2 (nand_2_out, ABCD[2], ABCD[2]);
  nand nand_3 (nand_3_out, ABCD[0], ABCD[0]);
  nand nand_4 (nand_4_out, nand_1_out, ABCD[1]);
  nand nand_5 (nand_5_out, ABCD[1], nand_2_out);
  nand nand_6 (nand_6_out, ABCD[3], ABCD[2], nand_3_out);
  nand nand_7 (S, nand_4_out, nand_5_out, nand_6_out);

  // Notes on the sheet:
  //   Jonathan Felipe Matricula 415704
endmodule
