// Logisim project Exercicio05_Logisim.circ as structural Verilog: 2 circuits, main circuit Simpilicado
module main (
  input  [3:0] ABCD,
  output S
);

  wire nor_1_out, nor_2_out, nor_3_out, nor_4_out, nor_5_out, nor_6_out, nor_7_out, nor_8_out;

  nor nor_1 (nor_1_out, ABCD[3], ABCD[3]);
  nor nor_2 (nor_2_out, ABCD[0], ABCD[0]);
  nor nor_3 (nor_3_out, ABCD[3], ABCD[2], ABCD[1]);
  nor nor_4 (nor_4_out, nor_1_out, ABCD[2], ABCD[1]);
  nor nor_5 (nor_5_out, nor_1_out, ABCD[1], nor_2_out);
  nor nor_6 (nor_6_out, ABCD[3], ABCD[1], ABCD[0]);
  nor nor_7 (nor_7_out, nor_1_out, ABCD[2], nor_2_out);
  nor nor_8 (nor_8_out, nor_3_out, nor_4_out, nor_5_out, nor_6_out, nor_7_out);
  nor nor_9 (S, nor_8_out, nor_8_out);

  // Notes on the sheet:
  //   Jonathan Felipe Matricula 415704
endmodule

module Simpilicado (
  input  [3:0] ABCD,
  output S
);

  wire nor_1_out, nor_2_out, nor_3_out, nor_4_out, nor_5_out, nor_6_out, nor_7_out, nor_8_out;

  nor nor_1 (nor_1_out, ABCD[3], ABCD[3]);
  nor nor_2 (nor_2_out, ABCD[0], ABCD[0]);
  nor nor_3 (nor_3_out, ABCD[3], ABCD[2], ABCD[1]);
  nor nor_4 (nor_4_out, nor_1_out, ABCD[2], ABCD[1]);
  nor nor_5 (nor_5_out, nor_1_out, ABCD[1], nor_2_out);
  nor nor_6 (nor_6_out, ABCD[3], ABCD[1], ABCD[0]);
  nor nor_7 (nor_7_out, nor_1_out, ABCD[2], nor_2_out);
  nor nor_8 (nor_8_out, nor_3_out, nor_4_out, nor_5_out, nor_6_out, nor_7_out);
  nor nor_9 (S, nor_8_out, nor_8_out);

  // Notes on the sheet:
  //   Jonathan Felipe Matricula 415704
endmodule
