// Logisim project Exercicio01_Guia08.circ as structural Verilog
module Exercicio02_guia08 (
  input  a,
  input  b,
  input  c,
  input  d,
  output out_5
);

  wire and_1_out, and_2_out, and_3_out, and_4_out, and_5_out, not_1_out, not_2_out, not_3_out, not_4_out,
       not_5_out, not_6_out, not_7_out, not_8_out, not_9_out, not_10_out, not_11_out;

  not not_1 (not_1_out, a);
  not not_2 (not_2_out, b);
  not not_3 (not_3_out, d);
  not not_4 (not_4_out, a);
  not not_5 (not_5_out, c);
  not not_6 (not_6_out, d);
  not not_7 (not_7_out, b);
  not not_8 (not_8_out, c);
  not not_9 (not_9_out, d);
  not not_10 (not_10_out, b);
  not not_11 (not_11_out, c);
  and and_1 (and_1_out, not_1_out, not_2_out, not_3_out);
  and and_2 (and_2_out, not_4_out, not_5_out, not_5_out, not_6_out);
  and and_3 (and_3_out, not_7_out, not_8_out, not_9_out);
  and and_4 (and_4_out, a, not_10_out, d);
  and and_5 (and_5_out, a, not_11_out, d);
  or or_1 (out_5, and_1_out, and_2_out, and_3_out, and_4_out, and_5_out);

  // Notes on the sheet:
  //   MARCOS FELIPE MARTINS SILVA_415719
  //   Exercicio02
endmodule

module Exercicio01_guia08 (
  input  a,
  input  b,
  input  c,
  input  d,
  output \saída 
);

  wire and_1_out, and_2_out, and_3_out, not_1_out, not_2_out, not_3_out;

  not not_1 (not_1_out, a);
  and and_1 (and_1_out, not_1_out, c);
  and and_2 (and_2_out, a, b, not_2_out);
  not not_2 (not_2_out, d);
  not not_3 (not_3_out, b);
  and and_3 (and_3_out, not_3_out, c);
  or or_1 (\saída , and_1_out, and_2_out, and_3_out, and_3_out);

  // Notes on the sheet:
  //   Exercicio01
  //   MARCOS FELIPE MARTINS SILVA_415719
endmodule

module Exercicio03_guia08 (
  input  a,
  input  b,
  input  c,
  input  d,
  output out_5
);

  wire and_1_out, and_2_out, and_3_out, and_4_out, and_5_out, not_1_out, not_2_out, not_3_out, not_4_out,
       not_5_out, not_6_out, not_7_out, not_8_out, not_9_out, not_10_out;

  not not_1 (not_1_out, a);
  not not_2 (not_2_out, b);
  not not_3 (not_3_out, d);
  not not_4 (not_4_out, a);
  not not_5 (not_5_out, c);
  not not_6 (not_6_out, d);
  not not_7 (not_7_out, b);
  not not_8 (not_8_out, c);
  not not_9 (not_9_out, c);
  not not_10 (not_10_out, b);
  and and_1 (and_1_out, not_1_out, not_2_out, not_3_out);
  and and_2 (and_2_out, not_4_out, not_5_out, not_5_out, not_6_out);
  and and_3 (and_3_out, a, not_7_out, not_8_out);
  and and_4 (and_4_out, a, not_9_out, d);
  and and_5 (and_5_out, a, not_10_out, d);
  or or_1 (out_5, and_1_out, and_2_out, and_3_out, and_4_out, and_5_out);

  // Notes on the sheet:
  //   MARCOS FELIPE MARTINS SILVA_415719
  //   Exercicio03
endmodule

module Exercicio04_guia08 (
  input  a,
  input  b,
  input  c,
  input  d,
  output out_5
);

  wire nand_1_out, nand_2_out, nand_3_out, nand_4_out, nand_5_out, nand_6_out;

  nand nand_1 (nand_1_out, a, a);
  nand nand_2 (nand_2_out, d, d);
  nand nand_3 (nand_3_out, b, b, b);
  nand nand_4 (nand_4_out, nand_1_out, c);
  nand nand_5 (nand_5_out, a, b, nand_2_out);
  nand nand_6 (nand_6_out, nand_3_out, c);
  nand nand_7 (out_5, nand_4_out, nand_5_out, nand_6_out);

  // Notes on the sheet:
  //   MARCOS FELIPE MARTINS SILVA_415719
  //   Exercicio04
endmodule
