// Logisim project Exe05.circ as structural Verilog: 4 circuits, main circuit main
module main (
  input  a,
  input  b,
  input  c,
  input  d,
  output s0
);

  wire andgate_1_out_4, andgate_2_out_4, andgate_3_out_4, andgate_4_out_4, andgate_5_out_4, notgate_1_out_2,
       notgate_2_out_2, notgate_3_out_2, notgate_4_out_2, notgate_5_out_2, notgate_6_out_2, notgate_7_out_2,
       notgate_8_out_2, notgate_9_out_2, notgate_10_out_2, notgate_11_out_2;

  notgate notgate_1 (.in_1(a), .out_2(notgate_1_out_2));
  notgate notgate_2 (.in_1(b), .out_2(notgate_2_out_2));
  notgate notgate_3 (.in_1(d), .out_2(notgate_3_out_2));
  notgate notgate_4 (.in_1(a), .out_2(notgate_4_out_2));
  notgate notgate_5 (.in_1(c), .out_2(notgate_5_out_2));
  notgate notgate_6 (.in_1(d), .out_2(notgate_6_out_2));
  notgate notgate_7 (.in_1(b), .out_2(notgate_7_out_2));
  notgate notgate_8 (.in_1(c), .out_2(notgate_8_out_2));
  notgate notgate_9 (.in_1(d), .out_2(notgate_9_out_2));
  notgate notgate_10 (.in_1(b), .out_2(notgate_10_out_2));
  notgate notgate_11 (.in_1(c), .out_2(notgate_11_out_2));
  andgate andgate_1 (.in_1(notgate_1_out_2), .in_2(notgate_2_out_2), .in_3(notgate_3_out_2), .out_4(andgate_1_out_4));
  andgate andgate_2 (.in_1(notgate_4_out_2), .in_2(notgate_5_out_2), .in_3(notgate_6_out_2), .out_4(andgate_2_out_4));
  andgate andgate_3 (.in_1(notgate_7_out_2), .in_2(notgate_8_out_2), .in_3(notgate_9_out_2), .out_4(andgate_3_out_4));
  andgate andgate_4 (.in_1(a), .in_2(notgate_10_out_2), .in_3(d), .out_4(andgate_4_out_4));
  andgate andgate_5 (.in_1(a), .in_2(notgate_11_out_2), .in_3(d), .out_4(andgate_5_out_4));
  orgate orgate_1 (
    .in_1(andgate_1_out_4), .in_2(andgate_2_out_4), .in_3(andgate_3_out_4), .in_4(andgate_4_out_4),
    .in_5(andgate_5_out_4), .out_6(s0));
endmodule

module andgate (
  input  in_1,
  input  in_2,
  input  in_3,
  output out_4
);

  wire nor_1_out, nor_2_out, nor_3_out;

  nor nor_1 (nor_1_out, in_1, in_1);
  nor nor_2 (nor_2_out, in_2, in_2);
  nor nor_3 (nor_3_out, in_3, in_3);
  nor nor_4 (out_4, nor_1_out, nor_2_out, nor_3_out);
endmodule

module notgate (
  input  in_1,
  output out_2
);

  nor nor_1 (out_2, in_1, in_1);
endmodule

module orgate (
  input  in_1,
  input  in_2,
  input  in_3,
  input  in_4,
  input  in_5,
  output out_6
);

  wire nor_1_out;

  nor nor_1 (nor_1_out, in_1, in_2, in_3, in_4, in_5);
  nor nor_2 (out_6, nor_1_out, nor_1_out, nor_1_out, nor_1_out, nor_1_out);
endmodule
