// Logisim project geradordepulmetfreq.circ as structural Verilog: 1 circuit, main circuit geradordepulmetfreq.circ
module geradordepulmetfreq_circ (
  input  D,
  input  B,
  input  C,
  input  A,
  output SAIDA1,
  output out_6
);

  wire undriven, undriven_2, undriven_3, undriven_4, xor_1_out, xor_2_out, xor_3_out;

  Clock #(.highDuration(1), .lowDuration(1)) clock_1 ();  // open: out
  ExactlyOne xor_1 (.out(xor_1_out), .in0(undriven_4), .in1(undriven_3), .in2(undriven_2), .in3(A), .in4(undriven));
  ExactlyOne xor_2 (.out(xor_2_out), .in1(xor_1_out), .in2(undriven_3), .in3(undriven_4), .in4(undriven_2));
  ExactlyOne xor_3 (.out(xor_3_out), .in1(xor_2_out), .in2(undriven_3), .in3(undriven), .in4(undriven_4));
  not not_1 (out_6, xor_3_out);
  or or_1 (SAIDA1, xor_1_out, xor_3_out);

  // Notes on the sheet:
  //   CLOC
  //   eneas,numero:376507
  //   SAIDA2
endmodule
