// Logisim project exercicio01.circ as structural Verilog: 1 circuit, main circuit main
module main (
  output out_1
);

  wire clock_1_out;

  Clock #(.highDuration(1), .lowDuration(1)) clock_1 (.out(clock_1_out));
  T_Flip_Flop #(.trigger("rising")) t_ff_1 (.clk(clock_1_out), .T(1'b1), .Q(out_1));  // open: Qn, preset, reset, en

  // Notes on the sheet:
  //   Guia 09 - Exercicio 01
  //   Tiago Menegaz de Melo Garcia 405844
endmodule
