// Logisim project Exercicio01_Logisim.circ as structural Verilog: 1 circuit, main circuit main
module main (
);

  wire clock_1_out, t_ff_1_q;

  Clock #(.highDuration(1), .lowDuration(1)) clock_1 (.out(clock_1_out));
  LED #(.active("true")) led_1 (.in(t_ff_1_q));
  T_Flip_Flop #(.trigger("rising")) t_ff_1 (.clk(clock_1_out), .T(1'b1), .Q(t_ff_1_q));  // open: Qn, preset, reset, en

  // Notes on the sheet:
  //   Jonathan Felipe Xavier  Matricula: 415704
endmodule
