// Logisim project Exercicio01_guia09.circ as structural Verilog: 1 circuit, main circuit main
module main (
  output out_1
);

  wire clock_1_out;

  Clock #(.highDuration(8), .lowDuration(1)) clock_1 (.out(clock_1_out));
  T_Flip_Flop #(.trigger("rising")) t_ff_1 (.clk(clock_1_out), .T(1'b1), .Q(out_1));  // open: Qn, preset, reset, en

  // Notes on the sheet:
  //   Exercicio01_guia09
  //   Marcos Felipe Martins Silva_415719
endmodule
