// Logisim project exercicio01.circ as structural Verilog: 1 circuit, main circuit main
module main (
  output out_1
);

  wire clock_1_out;

  T_Flip_Flop #(.trigger("rising")) t_ff_1 (.clk(clock_1_out), .T(1'b1), .Q(out_1));  // open: Qn, preset, reset, en
  Clock #(.highDuration(6), .lowDuration(6)) clock_1 (.out(clock_1_out));

  // Notes on the sheet:
  //   Exercicio 01
  //   Henrique Carvalho Parreira
endmodule
