// Logisim project Guia1001.circ as structural Verilog: 1 circuit, main circuit main
module main (
  input  S,
  input  R,
  output Q,
  output Q_prime
);

  nor nor_1 (Q, S, Q_prime);
  nor nor_2 (Q_prime, Q, R);

  // Notes on the sheet:
  //   Andre Sulivam 391998
endmodule
