// Logisim project Guia1002.circ as structural Verilog: 1 circuit, main circuit main
module main (
  input  PR_prime,
  input  S,
  input  C,
  input  R,
  input  CL_prime,
  output Q,
  output Q_prime
);

  wire nand_1_out, nand_2_out;

  nand nand_1 (nand_1_out, S, C);
  nand nand_2 (nand_2_out, C, R);
  nand nand_3 (Q, PR_prime, nand_1_out, Q_prime);
  nand nand_4 (Q_prime, Q, nand_2_out, CL_prime);

  // Notes on the sheet:
  //   Andre Sulivam 391998
endmodule
