// Logisim project guia10.circ as structural Verilog: 3 circuits, main circuit Latch SR
module Latch_SR (
  input  S,
  input  R,
  output Q0,
  output Q
);

  nor nor_1 (Q0, S, Q);
  nor nor_2 (Q, Q0, R);

  // Notes on the sheet:
  //   Nome: Danie Sathler Silva
  //   Matrícula:405795
endmodule

module Latch_SR__nand (
  input  S,
  input  R,
  output Q0,
  output Q
);

  nand nand_1 (Q0, S, Q);
  nand nand_2 (Q, Q0, R);

  // Notes on the sheet:
  //   Nome: Danie Sathler Silva
  //   Matrícula:405795
endmodule

module Latch_D (
  input  D,
  input  E,
  output Q,
  output Q0
);

  wire nand_1_out, nand_2_out, not_1_out;

  not not_1 (not_1_out, D);
  nand nand_1 (nand_1_out, D, E);
  nand nand_2 (nand_2_out, not_1_out, E);
  Latch_SR latch_sr_1 (.S(nand_1_out), .R(nand_2_out), .Q0(Q), .Q(Q0));

  // Notes on the sheet:
  //   Nome: Danie Sathler Silva
  //   Matrícula:405795
endmodule
