// Logisim project Guia10.circ as structural Verilog
module Latch_SR___NOR (
  input  S,
  input  R,
  output Q,
  output Q_prime
);

  nor nor_1 (Q_prime, S, Q);
  nor nor_2 (Q, Q_prime, R);

  // Notes on the sheet:
  //   Matricula: 405804
  //   Nome: Gustavo Guimarães
endmodule

module Latch_SR___NAND_PRESET_CL (
  input  Preset,
  input  S,
  input  R,
  input  Clear,
  input  Enable,
  output Q,
  output Q_prime
);

  wire nand_1_out, nand_2_out;

  nand nand_1 (nand_1_out, S, Enable);
  nand nand_2 (nand_2_out, Enable, R);
  nand nand_3 (Q, Preset, nand_1_out, Q_prime);
  nand nand_4 (Q_prime, Q, nand_2_out, Clear);

  // Notes on the sheet:
  //   Matricula: 405804
  //   Nome: Gustavo Guimarães
endmodule

module Latch_D___NAND_PRESET_CLEAR (
  input  Preset,
  input  D,
  input  Enable,
  input  Clear,
  output Q,
  output Q_prime
);

  wire nand_1_out, nand_2_out, not_1_out;

  not not_1 (not_1_out, D);
  nand nand_1 (nand_1_out, D, Enable);
  nand nand_2 (nand_2_out, Enable, not_1_out);
  nand nand_3 (Q, Preset, nand_1_out, Q_prime);
  nand nand_4 (Q_prime, Q, nand_2_out, Clear);

  // Notes on the sheet:
  //   Matricula: 405804
  //   Nome: Gustavo Guimarães
endmodule
