// Logisim project guia_10.circ as structural Verilog: 4 circuits, main circuit Ex_01
module Ex_01 (
  input  S,
  input  R,
  output Q_prime,
  output Q
);

  nor nor_1 (Q_prime, S, Q);
  nor nor_2 (Q, Q_prime, R);

  // Notes on the sheet:
  //   405807
  //   J. Erimá F. Júnior
endmodule

module Ex_02_04 (
  input  preset,
  input  S,
  input  R,
  input  clear,
  output Q,
  output Q_prime
);

  nand nand_1 (Q, preset, S, Q_prime);
  nand nand_2 (Q_prime, Q, R, clear);
endmodule

module Ex_03 (
  input  preset,
  input  D,
  input  reset,
  output Q,
  output Q_prime
);

  wire not_1_out;

  not not_1 (not_1_out, D);
  nand nand_1 (Q, preset, D, Q_prime);
  nand nand_2 (Q_prime, Q, not_1_out, reset);
endmodule

module Ex_05 (
  input  R,
  output Q,
  output Q_prime
);

  wire not_1_out;

  not not_1 (not_1_out, R);
  nor nor_1 (Q, R, Q_prime);
  nor nor_2 (Q_prime, Q, not_1_out);
endmodule
