// Logisim project Guia1001.circ as structural Verilog: 1 circuit, main circuit main
module main (
  input  R,
  input  S,
  output Q,
  output nQ
);

  nor nor_1 (Q, R, nQ);
  nor nor_2 (nQ, Q, S);

  // Notes on the sheet:
  //   Luiz Felipe Fonseca - 405817
endmodule
