// Logisim project Guia1002.circ as structural Verilog: 1 circuit, main circuit main
module main (
  input  Preset,
  input  S,
  input  R,
  input  Clear,
  output Q,
  output nQ
);

  nand nand_1 (Q, S, Preset, nQ);
  nand nand_2 (nQ, Q, Clear, R);

  // Notes on the sheet:
  //   Luiz Felipe Fonseca - 405817
endmodule
