// Logisim project latch_circuit.circ as structural Verilog: 5 circuits, main circuit latch_SR_nor
module latch_SR_nor (
  input  S,
  input  R,
  output Q_prime,
  output Q
);

  nor nor_1 (Q_prime, S, Q);
  nor nor_2 (Q, Q_prime, R);

  // Notes on the sheet:
  //   Márcia Cibele Martins Carneiro - 404591
  //   Latch SR com portas NOR
endmodule

module latch_SR_nand (
  input  PR,
  input  S,
  input  R,
  input  CL,
  output Q,
  output Q_prime
);

  wire nand_1_out, nand_2_out, undriven;

  nand nand_1 (nand_1_out, S, undriven);
  nand nand_2 (nand_2_out, undriven, R);
  nand nand_3 (Q, nand_1_out, PR, Q_prime);
  nand nand_4 (Q_prime, Q, CL, nand_2_out);

  // Notes on the sheet:
  //   Márcia Cibele Martins Carneiro - 404591
  //   Latch SR com portas NAND, com PRESET e CLEAR
endmodule

module latch_D_NAND (
  input  PR_prime,
  input  D,
  input  CL_prime,
  output Q,
  output Q_prime
);

  wire nand_1_out, nand_2_out, not_1_out, undriven;

  not not_1 (not_1_out, D);
  nand nand_1 (nand_1_out, D, undriven);
  nand nand_2 (nand_2_out, undriven, not_1_out);
  nand nand_3 (Q, nand_1_out, PR_prime, Q_prime);
  nand nand_4 (Q_prime, Q, CL_prime, nand_2_out);

  // Notes on the sheet:
  //   Márcia Cibele Martins Carneiro - 404591
  //   Latch D com portas NAND, PRESET e CLEAR
endmodule

module latch_D_a_partir_SR (
  input  D,
  output Q,
  output Q_prime
);

  wire not_1_out;

  not not_1 (not_1_out, D);
  // latch_SR_sem_PRESET_CLEAR latch_sr_sem_preset_clear_1: pin names not known; wires that end beside it: D, not_1_out, Q, Q_prime

  // Notes on the sheet:
  //   Márcia Cibele Martins Carneiro - 404591
  //   Latch D a partir de um latch SR sem PRESET e CLEAR
endmodule

module latch_SR_sem_PRESET_CLEAR (
  input  S_prime,
  input  R_prime,
  output Q,
  output Q_prime
);

  wire nand_1_out, nand_2_out, undriven;

  nand nand_1 (nand_1_out, S_prime, undriven);
  nand nand_2 (nand_2_out, undriven, R_prime);
  nand nand_3 (Q, nand_1_out, Q_prime);
  nand nand_4 (Q_prime, Q, nand_2_out);

  // Notes on the sheet:
  //   Márcia Cibele Martins Carneiro - 404591
  //   Latch D com portas NAND, sem PRESET e CLEAR
endmodule
