// Logisim project Ex02.circ as structural Verilog: 1 circuit, main circuit main
module main (
  input  Preset,
  input  S,
  input  C,
  input  R,
  input  Clear,
  output Q,
  output nQ
);

  wire nand_1_out, nand_2_out;

  nand nand_1 (nand_1_out, S, C);
  nand nand_2 (nand_2_out, C, R);
  nand nand_3 (Q, nand_1_out, Preset, nQ);
  nand nand_4 (nQ, Q, Clear, nand_2_out);
endmodule
