// Logisim project circuitos.circ as structural Verilog: 6 circuits, main circuit main
module main (
  input  S,
  input  R,
  input  PR,
  input  CL,
  input  D,
  output Q_prime_1,
  output Q1,
  output Q2,
  output Q_prime_2,
  output Q3,
  output Q_prime_3,
  output Q4,
  output Q_prime_4,
  output Q5,
  output Q_prime_5
);

  numero_01 numero_01_1 (.S(S), .R(R), .Q_prime(Q_prime_1), .Q(Q1));
  numero_02 numero_02_1 (.S(S), .R(R), .Q(Q2), .Q_prime(Q_prime_2));
  numero_03 numero_03_1 (.D(D), .PR(PR), .CL(CL), .Q(Q3), .Q_prime(Q_prime_3));
  numero_04 numero_04_1 (.S(S), .R(R), .PR(PR), .CL(CL), .Q(Q4), .Q_prime(Q_prime_4));
  numero_05 numero_05_1 (.D(D), .Q(Q5), .Q_prime(Q_prime_5));

  // Notes on the sheet:
  //   numero_01
  //   numero_02
  //   numero_05
  //   numero_03
  //   numero_04
endmodule

module numero_01 (
  input  S,
  input  R,
  output Q_prime,
  output Q
);

  nor nor_1 (Q_prime, S, Q);
  nor nor_2 (Q, Q_prime, R);
endmodule

module numero_02 (
  input  S,
  input  R,
  output Q,
  output Q_prime
);

  nand nand_1 (Q, S, Q_prime);
  nand nand_2 (Q_prime, Q, R);
endmodule

module numero_03 (
  input  PR,
  input  D,
  input  CL,
  output Q,
  output Q_prime
);

  wire not_1_out;

  not not_1 (not_1_out, D);
  nand nand_1 (Q, D, PR, Q_prime);
  nand nand_2 (Q_prime, Q, CL, not_1_out);
endmodule

module numero_04 (
  input  PR,
  input  S,
  input  R,
  input  CL,
  output Q,
  output Q_prime
);

  nand nand_1 (Q, S, PR, Q_prime);
  nand nand_2 (Q_prime, Q, CL, R);
endmodule

module numero_05 (
  input  D,
  output Q,
  output Q_prime
);

  wire not_1_out;

  not not_1 (not_1_out, D);
  numero_02 numero_02_1 (.S(D), .R(not_1_out), .Q(Q), .Q_prime(Q_prime));
endmodule
