// Logisim project implementacao01.circ as structural Verilog: 1 circuit, main circuit main
module main (
  input  Set,
  input  Reset,
  output Q,
  output Q_prime
);

  nor nor_1 (Q_prime, Set, Q);
  nor nor_2 (Q, Q_prime, Reset);

  // Notes on the sheet:
  //   Guia 10 - Implementação01
  //   Tiago Menegaz de Melo Garcia     405844
  //   Implementar um Lacth SR com portas NOR
endmodule
