// Logisim project implementacao02.circ as structural Verilog: 1 circuit, main circuit main
module main (
  input  PRESET,
  input  Set,
  input  CLEAR,
  input  Reset,
  input  CLEAR1,
  output Q,
  output Q_prime
);

  wire nand_1_out, nand_2_out;

  nand nand_1 (nand_1_out, Set, CLEAR);
  nand nand_2 (nand_2_out, CLEAR, Reset);
  nand nand_3 (Q, PRESET, nand_1_out, Q_prime);
  nand nand_4 (Q_prime, Q, nand_2_out, CLEAR1);

  // Notes on the sheet:
  //   Guia 10 - Implementação02
  //   Tiago Menegaz de Melo Garcia     405844
  //   Implementar um Lacth SR com portas NAND, PRESET e CLEAR
endmodule
