// Logisim project implementacao03.circ as structural Verilog: 1 circuit, main circuit main
module main (
  input  PRESET,
  input  D,
  input  C,
  input  CLEAR_prime,
  output Q,
  output Q_prime
);

  wire nand_1_out, nand_2_out, nand_3_out;

  not nand_1 (nand_1_out, D);  // NAND_Gate
  nand nand_2 (nand_2_out, D, C);
  nand nand_3 (nand_3_out, C, nand_1_out);
  nand nand_4 (Q, PRESET, nand_2_out, Q_prime);
  nand nand_5 (Q_prime, Q, nand_3_out, CLEAR_prime);

  // Notes on the sheet:
  //   Tiago Menegaz de Melo Garcia     405844
  //   Guia 10 - Implementação 03
  //   Implementar um Lacth D com portas NAND, PRESET e CLEAR
endmodule
