// Logisim project guia10 - 412727.circ as structural Verilog: 6 circuits, main circuit main
module main (
  input  s,
  input  r,
  input  pr,
  input  clr,
  output out_5,
  output Ex1,
  output Ex2,
  output out_8,
  output Ex3,
  output out_10,
  output Ex4,
  output out_12,
  output out_13,
  output Ex5
);

  Exercicio_1 exercicio_1_1 (.set(s), .reset(r), .q(out_5), .nq(Ex1));
  Exercicio_2 exercicio_2_1 (.s(s), .c(clr), .r(r), .pr(pr), .cl(1'b1), .nq(Ex2), .q(out_8));
  Exercicio_3 exercicio_3_1 (.d(s), .c(r), .pr(pr), .cl(1'b1), .nq(Ex3), .q(out_10));
  Exercicio_4 exercicio_4_1 (.s(s), .c(clr), .r(r), .pr(pr), .cl(1'b1), .nq(Ex4), .q(out_12));
  Exercicio_5 exercicio_5_1 (.d(s), .q(out_13), .nq(Ex5));

  // Notes on the sheet:
  //   c
  //   AUGUSTO FERREIRA ANDRADE DO CARMO - 412727
endmodule

module Exercicio_1 (
  input  set,
  input  reset,
  output q,
  output nq
);

  nor nor_1 (nq, set, q);
  nor nor_2 (q, nq, reset);

  // Notes on the sheet:
  //   s r e
  //   0 0 hold
  //   0 1 reset
  //   1 0 set
  //   11 x
endmodule

module Exercicio_2 (
  input  pr,
  input  s,
  input  c,
  input  r,
  input  cl,
  output nq,
  output q
);

  wire nand_1_out, nand_2_out, not_1_out, not_2_out;

  nand nand_1 (nand_1_out, c, s);
  nand nand_2 (nand_2_out, r, c);
  not not_1 (not_1_out, pr);
  not not_2 (not_2_out, cl);
  nand nand_3 (nq, not_1_out, q, nand_1_out);
  nand nand_4 (q, nq, nand_2_out, not_2_out);
endmodule

module Exercicio_3 (
  input  pr,
  input  d,
  input  c,
  input  cl,
  output nq,
  output q
);

  wire nand_1_out, nand_2_out, not_1_out, not_2_out, not_3_out;

  not not_1 (not_1_out, d);
  nand nand_1 (nand_1_out, c, d);
  nand nand_2 (nand_2_out, not_1_out, c);
  not not_2 (not_2_out, pr);
  not not_3 (not_3_out, cl);
  nand nand_3 (nq, not_2_out, q, nand_1_out);
  nand nand_4 (q, nq, nand_2_out, not_3_out);
endmodule

module Exercicio_4 (
  input  pr,
  input  s,
  input  c,
  input  r,
  input  cl,
  output nq,
  output q
);

  wire nand_1_out, nand_2_out, not_1_out, not_2_out;

  nand nand_1 (nand_1_out, c, s);
  nand nand_2 (nand_2_out, r, c);
  not not_1 (not_1_out, pr);
  not not_2 (not_2_out, cl);
  nand nand_3 (nq, not_1_out, q, nand_1_out);
  nand nand_4 (q, nq, nand_2_out, not_2_out);

  // Notes on the sheet:
  //   Mesma coisa do Exercicio2
endmodule

module Exercicio_5 (
  input  d,
  output q,
  output nq
);

  wire not_1_out;

  not not_1 (not_1_out, d);
  nand nand_1 (nq, d, q);
  nand nand_2 (q, nq, not_1_out);
endmodule
