// Logisim project circuitos.circ as structural Verilog: 6 circuits, main circuit main
module main (
  input  S,
  input  R,
  input  PR,
  input  CL,
  input  D,
  output Q_prime_1,
  output Q1,
  output Q2,
  output Q_prime_2,
  output Q3,
  output Q_prime_3,
  output Q4,
  output Q_prime_4,
  output Q5,
  output Q_prime_5
);

  Exercicio01 exercicio01_1 (.S(S), .R(R), .Q_prime(Q_prime_1), .Q(Q1));
  Exercicio02 exercicio02_1 (.S(S), .R(R), .Q(Q2), .Q_prime(Q_prime_2));
  Exercicio03 exercicio03_1 (.D(D), .PR(PR), .CL(CL), .Q(Q3), .Q_prime(Q_prime_3));
  Exercicio04 exercicio04_1 (.S(S), .R(R), .PR(PR), .CL(CL), .Q(Q4), .Q_prime(Q_prime_4));
  Exercicio05 exercicio05_1 (.D(D), .Q(Q5), .Q_prime(Q_prime_5));

  // Notes on the sheet:
  //   numero_01
  //   numero_02
  //   numero_05
  //   numero_03
  //   numero_04
endmodule

module Exercicio01 (
  input  S,
  input  R,
  output Q_prime,
  output Q
);

  nor nor_1 (Q_prime, S, Q);
  nor nor_2 (Q, Q_prime, R);
endmodule

module Exercicio02 (
  input  S,
  input  R,
  output Q,
  output Q_prime
);

  nand nand_1 (Q, S, Q_prime);
  nand nand_2 (Q_prime, Q, R);
endmodule

module Exercicio03 (
  input  PR,
  input  D,
  input  CL,
  output Q,
  output Q_prime
);

  wire not_1_out;

  not not_1 (not_1_out, D);
  nand nand_1 (Q, D, PR, Q_prime);
  nand nand_2 (Q_prime, Q, CL, not_1_out);
endmodule

module Exercicio04 (
  input  PR,
  input  S,
  input  R,
  input  CL,
  output Q,
  output Q_prime
);

  nand nand_1 (Q, S, PR, Q_prime);
  nand nand_2 (Q_prime, Q, CL, R);
endmodule

module Exercicio05 (
  input  D,
  output Q,
  output Q_prime
);

  wire not_1_out;

  not not_1 (not_1_out, D);
  Exercicio02 exercicio02_1 (.S(D), .R(not_1_out), .Q(Q), .Q_prime(Q_prime));
endmodule
