// Logisim project circuit lach SR.circ as structural Verilog: 1 circuit, main circuit circuit lach SR.circ
module circuit_lach_SR_circ (
  input  q,
  input  p,
  input  R,
  output s1,
  output s2
);

  wire clock_1_out, nor_1_out, nor_2_out;

  Clock #(.highDuration(1), .lowDuration(1)) clock_1 (.out(clock_1_out));
  nor nor_1 (nor_1_out, q, clock_1_out);
  nor nor_2 (nor_2_out, clock_1_out, p, R);
  S_R_Flip_Flop #(.trigger("rising")) s_r_ff_1 (
    .S(nor_1_out), .clk(clock_1_out), .R(nor_2_out), .Q(s1), .Qn(s2));  // open: preset, reset, en
  // Probe on s1
  // Probe on s2

  // Notes on the sheet:
  //   input
  //   input
  //   circuito lach SR
  //   out
  //   out
  //   Nome:Eneas 376507
endmodule
