// Logisim project exe02.circ as structural Verilog: 1 circuit, main circuit main
module main (
  input  set,
  input  clear,
  output Q,
  output Q_2
);

  nand nand_1 (Q, set, Q_2);
  nand nand_2 (Q_2, Q, clear);

  // Notes on the sheet:
  //   LATCH COM PORTAS NOR
  //   Set  | Clear | Saída
  //   0    |    0
  //   1    |    0      | Q = 1 
  //   0    |    1      | Q = 0 
  //   1    |    1      |  Inválido
  //   | Não muda
endmodule
