// Logisim project exe05.circ as structural Verilog: 4 circuits, main circuit main
module main (
  input  D,
  input  en,
  output Q,
  output Q_2
);

  wire nand_1_out, nand_2_out, not_1_out;

  nand nand_1 (nand_1_out, D, en);
  nand nand_2 (nand_2_out, en, not_1_out);
  not not_1 (not_1_out, D);
  nand nand_3 (Q, nand_1_out, Q_2);
  nand nand_4 (Q_2, Q, nand_2_out);

  // Notes on the sheet:
  //   LATCH D COM PORTAS NAND
  //   EN         D              |                Qi
  //   0           X              |                Q ( não muda )       
  //   1           0              |                 0
  //   1           1              |                 1  
  //    ENTRADAS         |       Saída
  //   ----------------------------------------------------
  //   ----------------------------------------------------
  //   "x" indica a condição "don't care"
  //   antes de EN ir para nível Baixo
  //   Qi é o estado de Q imediatamente
endmodule

module latch_D (
  input  in_1,
  input  in_2,
  output Q,
  output Q_2
);

  nand nand_1 (Q, in_1, Q_2);
  nand nand_2 (Q_2, Q, in_2);

  // Notes on the sheet:
  //   LATCH SR COM PORTAS NAND
  //   EN         D              |                Qi
  //   0           X              |                Q ( não muda )       
  //   1           0              |                 0
  //   1           1              |                 1  
  //    ENTRADAS         |       Saída
  //   ----------------------------------------------------
  //   ----------------------------------------------------
  //   "x" indica a condição "don't care"
  //   antes de EN ir para nível Baixo
  //   Qi é o estado de Q imediatamente
endmodule

module LATCH_D (
  input  D,
  input  en,
  output out_3,
  output out_4
);

  wire nand_1_out, nand_2_out, not_1_out;

  nand nand_1 (nand_1_out, D, en);
  nand nand_2 (nand_2_out, en, not_1_out);
  not not_1 (not_1_out, D);
  latch_D latch_d_1 (.in_1(nand_1_out), .in_2(nand_2_out), .Q(out_3), .Q_2(out_4));

  // Notes on the sheet:
  //   LATCH D
endmodule

module LATCH_SR (
  input  in_1,
  input  in_2,
  output Q,
  output Q_2
);

  nand nand_1 (Q, in_1, Q_2);
  nand nand_2 (Q_2, Q, in_2);

  // Notes on the sheet:
  //   LATCH SR COM PORTAS NAND
  //   EN         D              |                Qi
  //   0           X              |                Q ( não muda )       
  //   1           0              |                 0
  //   1           1              |                 1  
  //    ENTRADAS         |       Saída
  //   ----------------------------------------------------
  //   ----------------------------------------------------
  //   "x" indica a condição "don't care"
  //   antes de EN ir para nível Baixo
  //   Qi é o estado de Q imediatamente
endmodule
