// Logisim project exercicio01.circ as structural Verilog: 1 circuit, main circuit main
module main (
  input  in_1,
  input  in_2,
  output out_3,
  output out_4
);

  nor nor_1 (out_4, out_3, in_2);
  nor nor_2 (out_3, in_1, out_4);

  // Notes on the sheet:
  //   Exercicio 01-----Mariana do Amaral(405819)
endmodule
