// Logisim project Exercicios_Guia10.circ as structural Verilog
module Exercicio01 (
  input  SET,
  input  CLEAR,
  output Q_tilde,
  output Q
);

  nor nor_1 (Q_tilde, SET, Q);
  nor nor_2 (Q, Q_tilde, CLEAR);

  // Notes on the sheet:
  //   Exercício1_guia10
  //   Marcos Felipe Martins Silva-415719
endmodule

module Exercicio02 (
  input  SET,
  input  CLEAR,
  output Q_tilde,
  output Q
);

  nand nand_1 (Q_tilde, SET, Q);
  nand nand_2 (Q, Q_tilde, CLEAR);

  // Notes on the sheet:
  //   Exercício02_guia10
  //   Marcos Felipe Martins Silva-415719
endmodule

module Exercicio03 (
  input  D,
  input  ENABLE,
  output Q,
  output Q_tilde
);

  wire nand_1_out, nand_2_out, not_1_out;

  not not_1 (not_1_out, D);
  nand nand_1 (nand_1_out, D, ENABLE);
  nand nand_2 (nand_2_out, ENABLE, not_1_out);
  nand nand_3 (Q, nand_1_out, Q_tilde);
  nand nand_4 (Q_tilde, Q, nand_2_out);

  // Notes on the sheet:
  //   Exercício03-guia10
  //   CLEAR
  //   Marcos Felipe Martins Silva-415719
  //   SET
endmodule

module Exercicio04 (
  input  SET,
  input  CLEAR,
  output Q_tilde,
  output Q
);

  nand nand_1 (Q_tilde, SET, Q);
  nand nand_2 (Q, Q_tilde, CLEAR);

  // Notes on the sheet:
  //   Exercício04_guia10
  //   Marcos Felipe Martins Silva-415719
endmodule

module Exercicio05 (
  input  D,
  input  ENABLE,
  output out_3,
  output out_4
);

  wire nand_1_out, nand_2_out, not_1_out;

  not not_1 (not_1_out, D);
  nand nand_1 (nand_1_out, D, ENABLE);
  nand nand_2 (nand_2_out, ENABLE, not_1_out);
  Exercicio01 exercicio01_1 (.SET(nand_1_out), .CLEAR(nand_2_out), .Q_tilde(out_3), .Q(out_4));

  // Notes on the sheet:
  //   Exercício05_guia10
  //   Marcos Felipe Martins Silva-415719
endmodule
