// Logisim project Guia1101.circ as structural Verilog: 1 circuit, main circuit main
module main (
  input  S_prime,
  input  R_prime,
  output Q,
  output Q_prime
);

  nor nor_1 (Q, S_prime, Q_prime);
  nor nor_2 (Q_prime, Q, R_prime);

  // Notes on the sheet:
  //   HEnrique Carvalho Parreira - 347133
endmodule
