// Logisim project Guia1102.circ as structural Verilog: 1 circuit, main circuit main
module main (
  input  PR_prime,
  input  S_prime,
  input  C,
  input  R_prime,
  input  CL_prime,
  output Q,
  output Q_prime
);

  wire nand_1_out, nand_2_out;

  nand nand_1 (nand_1_out, S_prime, C);
  nand nand_2 (nand_2_out, C, R_prime);
  nand nand_3 (Q, nand_1_out, PR_prime, Q_prime);
  nand nand_4 (Q_prime, Q, CL_prime, nand_2_out);

  // Notes on the sheet:
  //   Henrique Carvalho Parreira - 347133
endmodule
