// Logisim project guia10_ex01.circ as structural Verilog: 1 circuit, main circuit main
module main (
  input  s,
  input  r,
  output nq,
  output q
);

  nor nor_1 (nq, s, q);
  nor nor_2 (q, nq, r);

  // Notes on the sheet:
  //   s1
  //   s2
endmodule
