// Logisim project guia10_ex02.circ as structural Verilog: 1 circuit, main circuit main
module main (
  input  PR,
  input  S,
  input  C,
  input  R,
  input  CL,
  output Q,
  output QNOT
);

  wire nand_1_out, nand_2_out;

  nand nand_1 (nand_1_out, S, C);
  nand nand_2 (nand_2_out, C, R);
  nand nand_3 (Q, nand_1_out, PR, QNOT);
  nand nand_4 (QNOT, Q, CL, nand_2_out);
endmodule
