// Logisim project guia10_ex03.circ as structural Verilog: 1 circuit, main circuit main
module main (
  input  D,
  input  C,
  output Q,
  output Qnot
);

  wire nand_1_out, nand_2_out, not_1_out;

  nand nand_1 (nand_1_out, D, C);
  nand nand_2 (nand_2_out, C, not_1_out);
  not not_1 (not_1_out, D);
  nand nand_3 (Q, nand_1_out, Qnot);
  nand nand_4 (Qnot, Q, nand_2_out);

  // Notes on the sheet:
  //   s2
  //   s1
  //   s4
  //   s3
  //   s5
endmodule
