// Logisim project guia10_ex05.circ as structural Verilog: 2 circuits, main circuit main
module main (
  input  in_1,
  output out_2,
  output out_3
);

  wire not_1_out;

  not not_1 (not_1_out, in_1);
  latchsr latchsr_1 (.s(in_1), .r(not_1_out), .nq(out_2), .q(out_3));
endmodule

module latchsr (
  input  s,
  input  r,
  output nq,
  output q
);

  nor nor_1 (nq, s, q);
  nor nor_2 (q, nq, r);

  // Notes on the sheet:
  //   s1
  //   s2
endmodule
