// Logisim project Guia10.circ as structural Verilog: 5 circuits, main circuit main
module main (
  input  S,
  input  D,
  input  R,
  input  Preset,
  input  S_2,
  input  R_2,
  input  Clear,
  input  Preset_2,
  input  D_2,
  input  Enable,
  input  Clear_2,
  output Q,
  output Q_2,
  output QNOT,
  output QNOT_2,
  output Q_3,
  output QNOT_3,
  output Q_4,
  output QNOT_4
);

  Ex01 ex01_1 (.S(S), .R(R), .Q(Q), .QNOT(QNOT));
  Ex02 ex02_1 (.S(S_2), .R(R_2), .Preset(Preset), .Clear(Clear), .Q(Q_3), .QNOT(QNOT_3));
  Ex03 ex03_1 (.D(D_2), .Enable(Enable), .Preset(Preset_2), .Clear(Clear_2), .Q(Q_4), .QNOT(QNOT_4));
  Ex05 ex05_1 (.in_1(D), .Q(Q_2), .QNOT(QNOT_2));

  // Notes on the sheet:
  //   guia10 - Nádia de Souza Maciel Vieira Ferreira
endmodule

module Ex01 (
  input  S,
  input  R,
  output Q,
  output QNOT
);

  nor nor_1 (QNOT, S, Q);
  nor nor_2 (Q, QNOT, R);

  // Notes on the sheet:
  //   nadia de souza maciel vieira ferreira
endmodule

module Ex02 (
  input  Preset,
  input  S,
  input  R,
  input  Clear,
  output Q,
  output QNOT
);

  wire nand_1_out, nand_2_out, nand_3_out, nand_4_out, nand_6_out, nand_7_out;

  not nand_1 (nand_1_out, S);  // NAND_Gate
  not nand_2 (nand_2_out, Q);  // NAND_Gate
  not nand_3 (nand_3_out, QNOT);  // NAND_Gate
  not nand_4 (nand_4_out, R);  // NAND_Gate
  nand nand_5 (QNOT, Preset, nand_6_out);
  nand nand_6 (nand_6_out, nand_1_out, nand_2_out);
  nand nand_7 (nand_7_out, nand_3_out, nand_4_out);
  nand nand_8 (Q, nand_7_out, Clear);

  // Notes on the sheet:
  //   NOR = NAND(OR)
  //   OR = NAND( NAND(A), NAND(B) )
  //   Nádia de Souza Maciel Vieira Ferreira
endmodule

module Ex03 (
  input  Preset,
  input  D,
  input  Enable,
  input  Clear,
  output Q,
  output QNOT
);

  wire nand_1_out, nand_2_out, not_1_out;

  nand nand_1 (nand_1_out, D, Enable);
  nand nand_2 (nand_2_out, Enable, not_1_out);
  not not_1 (not_1_out, D);
  nand nand_3 (QNOT, nand_1_out, Preset, Q);
  nand nand_4 (Q, QNOT, Clear, nand_2_out);
endmodule

module Ex05 (
  input  in_1,
  output Q,
  output QNOT
);

  wire not_1_out;

  Ex01 ex01_1 (.S(in_1), .R(not_1_out), .Q(Q), .QNOT(QNOT));
  not not_1 (not_1_out, in_1);

  // Notes on the sheet:
  //   Nádia de Souza Maciel Vieira Ferreira
endmodule
