// Logisim project Exe02.circ as structural Verilog: 1 circuit, main circuit main
module main (
  input  Preset,
  input  D,
  input  Clk,
  input  Clear,
  output Q,
  output nQ
);

  wire nand_1_out, nand_2_out, not_1_out;

  not not_1 (not_1_out, D);
  nand nand_1 (nand_1_out, D, Clear, Clk, Clk);
  nand nand_2 (nand_2_out, Clk, Preset, not_1_out);
  nand nand_3 (Q, nand_1_out, Preset, nQ);
  nand nand_4 (nQ, Q, Clear, nand_2_out);

  // Notes on the sheet:
  //   Bruno César Lopes Silva - 415985
endmodule
