// Logisim project Exe03.circ as structural Verilog: 1 circuit, main circuit main
module main (
  input  Preset,
  input  S,
  input  R,
  input  Clear,
  output Q,
  output nQ
);

  nand nand_1 (Q, S, Preset, nQ);
  nand nand_2 (nQ, Q, Clear, R);

  // Notes on the sheet:
  //   Bruno César Lopes Silva - 415985
endmodule
