// Logisim project mealy_moore.circ as structural Verilog: 5 circuits, main circuit sequencia101 com intersecao
module sequencia101_com_intersecao (
  input  DATA,
  input  Reset,
  output S1
);

  wire Clock_out, d_ff_1_q, d_ff_2_q, d_ff_2_qn, d_ff_3_q, not_1_out;

  Clock #(.highDuration(1), .lowDuration(1)) Clock (.out(Clock_out));
  D_Flip_Flop #(.trigger("rising")) d_ff_1 (
    .clk(Clock_out), .D(DATA), .Q(d_ff_1_q), .reset(Reset));  // open: Qn, preset, en
  D_Flip_Flop #(.trigger("rising")) d_ff_2 (
    .clk(Clock_out), .D(d_ff_1_q), .Q(d_ff_2_q), .Qn(d_ff_2_qn), .reset(Reset));  // open: preset, en
  not not_1 (not_1_out, d_ff_2_qn);
  D_Flip_Flop #(.trigger("rising")) d_ff_3 (
    .clk(Clock_out), .D(d_ff_2_q), .Q(d_ff_3_q), .reset(Reset));  // open: Qn, preset, en
  and and_1 (S1, d_ff_1_q, not_1_out, d_ff_3_q);

  // Notes on the sheet:
  //   Márcia Cibele Martins Carneiro - 404591
  //   Márcia Cibele Martins Carneiro - 404591
  //   Mealy - FSM - sequencia(101)
endmodule

module sequencia_0101_sem_intersecao (
  input  DATA,
  input  Clear,
  output s
);

  wire and_1_out, CLK_out, d_ff_1_q, d_ff_1_qn, d_ff_2_q, d_ff_3_q, d_ff_3_qn, d_ff_4_q, d_ff_5_q, or_1_out;

  Clock #(.highDuration(1), .lowDuration(1)) CLK (.out(CLK_out));
  D_Flip_Flop #(.trigger("rising")) d_ff_1 (
    .clk(CLK_out), .D(DATA), .Q(d_ff_1_q), .Qn(d_ff_1_qn), .reset(or_1_out));  // open: preset, en
  or or_1 (or_1_out, Clear, d_ff_5_q);
  D_Flip_Flop #(.trigger("rising")) d_ff_2 (
    .clk(CLK_out), .D(d_ff_1_q), .Q(d_ff_2_q), .reset(or_1_out));  // open: Qn, preset, en
  D_Flip_Flop #(.trigger("rising")) d_ff_3 (
    .clk(CLK_out), .D(d_ff_2_q), .Q(d_ff_3_q), .Qn(d_ff_3_qn), .reset(or_1_out));  // open: preset, en
  and and_1 (and_1_out, d_ff_4_q, d_ff_3_qn, d_ff_2_q, d_ff_1_qn);
  D_Flip_Flop #(.trigger("rising")) d_ff_4 (
    .clk(CLK_out), .D(d_ff_3_q), .Q(d_ff_4_q), .reset(or_1_out));  // open: Qn, preset, en
  D_Flip_Flop #(.trigger("rising")) d_ff_5 (.clk(CLK_out), .D(and_1_out), .Q(d_ff_5_q));  // open: Qn, preset, en, reset
  D_Flip_Flop #(.trigger("rising")) d_ff_6 (.clk(CLK_out), .D(d_ff_5_q), .Q(s));  // open: Qn, preset, en, reset

  // Notes on the sheet:
  //   Márcia Cibele Martins Carneiro - 404591
  //   Márcia Cibele Martins Carneiro - 404591
  //   Moore - FSM - sequencia(0101)
endmodule

module sequencia_1001_com_intersecao (
  input  DATA,
  input  Clear,
  output s
);

  wire CLK_out, d_ff_1_q, d_ff_2_q, d_ff_3_q, d_ff_4_q, not_1_out, not_2_out;

  Clock #(.highDuration(1), .lowDuration(1)) CLK (.out(CLK_out));
  D_Flip_Flop #(.trigger("rising")) d_ff_1 (
    .clk(CLK_out), .D(DATA), .Q(d_ff_1_q), .reset(Clear));  // open: Qn, preset, en
  D_Flip_Flop #(.trigger("rising")) d_ff_2 (
    .clk(CLK_out), .D(d_ff_1_q), .Q(d_ff_2_q), .reset(Clear));  // open: Qn, preset, en
  D_Flip_Flop #(.trigger("rising")) d_ff_3 (
    .clk(CLK_out), .D(d_ff_2_q), .Q(d_ff_3_q), .reset(Clear));  // open: Qn, preset, en
  D_Flip_Flop #(.trigger("rising")) d_ff_4 (
    .clk(CLK_out), .D(d_ff_3_q), .Q(d_ff_4_q), .reset(Clear));  // open: Qn, preset, en
  not not_1 (not_1_out, d_ff_3_q);
  and and_1 (s, d_ff_4_q, not_1_out, not_2_out, d_ff_1_q);
  not not_2 (not_2_out, d_ff_2_q);

  // Notes on the sheet:
  //   Márcia Cibele Martins Carneiro - 404591
  //   Márcia Cibele Martins Carneiro - 404591
  //   Mealy - FSM - sequencia(0101)
endmodule

module sequencia_101_ou_010 (
  input  DATA,
  input  Clear,
  output s
);

  wire and_1_out, and_2_out, CLK_out, d_ff_1_q, d_ff_2_q, d_ff_3_q, not_1_out, not_2_out, not_3_out;

  Clock #(.highDuration(1), .lowDuration(1)) CLK (.out(CLK_out));
  D_Flip_Flop #(.trigger("rising")) d_ff_1 (
    .clk(CLK_out), .D(DATA), .Q(d_ff_1_q), .reset(Clear));  // open: Qn, preset, en
  D_Flip_Flop #(.trigger("rising")) d_ff_2 (
    .clk(CLK_out), .D(d_ff_1_q), .Q(d_ff_2_q), .reset(Clear));  // open: Qn, preset, en
  D_Flip_Flop #(.trigger("rising")) d_ff_3 (
    .clk(CLK_out), .D(d_ff_2_q), .Q(d_ff_3_q), .reset(Clear));  // open: Qn, preset, en
  and and_1 (and_1_out, d_ff_3_q, not_1_out, d_ff_1_q);
  not not_1 (not_1_out, d_ff_2_q);
  not not_2 (not_2_out, d_ff_3_q);
  not not_3 (not_3_out, d_ff_1_q);
  and and_2 (and_2_out, not_2_out, d_ff_2_q, not_3_out);
  or or_1 (s, and_2_out, and_1_out);

  // Notes on the sheet:
  //   Márcia Cibele Martins Carneiro - 404591
  //   Márcia Cibele Martins Carneiro - 404591
  //   Mealy - FSM - sequencia(101 ou 010)
endmodule

module sequencia_000_ou_111 (
  input  DATA,
  input  Clear,
  output s
);

  wire and_1_out, and_2_out, CLK_out, d_ff_1_q, d_ff_2_q, d_ff_3_q, not_1_out, not_2_out, not_3_out;

  Clock #(.highDuration(1), .lowDuration(1)) CLK (.out(CLK_out));
  D_Flip_Flop #(.trigger("rising")) d_ff_1 (
    .clk(CLK_out), .D(DATA), .Q(d_ff_1_q), .reset(Clear));  // open: Qn, preset, en
  D_Flip_Flop #(.trigger("rising")) d_ff_2 (
    .clk(CLK_out), .D(d_ff_1_q), .Q(d_ff_2_q), .reset(Clear));  // open: Qn, preset, en
  D_Flip_Flop #(.trigger("rising")) d_ff_3 (
    .clk(CLK_out), .D(d_ff_2_q), .Q(d_ff_3_q), .reset(Clear));  // open: Qn, preset, en
  not not_1 (not_1_out, d_ff_3_q);
  not not_2 (not_2_out, d_ff_2_q);
  not not_3 (not_3_out, d_ff_1_q);
  and and_1 (and_1_out, d_ff_3_q, d_ff_2_q, d_ff_1_q);
  and and_2 (and_2_out, not_1_out, not_2_out, not_3_out);
  or or_1 (s, and_2_out, and_1_out);

  // Notes on the sheet:
  //   Márcia Cibele Martins Carneiro - 404591
  //   Márcia Cibele Martins Carneiro - 404591
  //   Mealy - FSM - sequencia(000 ou 111)
endmodule
