// Logisim project Ex01.circ as structural Verilog: 1 circuit, main circuit main
module main (
  input  DATA,
  input  RST,
  output Out
);

  wire CLK_out, d_ff_1_q, d_ff_2_q, d_ff_3_q, not_1_out;

  Clock #(.highDuration(1), .lowDuration(1)) CLK (.out(CLK_out));
  D_Flip_Flop #(.trigger("rising")) d_ff_1 (
    .clk(CLK_out), .D(DATA), .Q(d_ff_1_q), .reset(RST));  // open: Qn, preset, en
  D_Flip_Flop #(.trigger("rising")) d_ff_2 (
    .clk(CLK_out), .D(d_ff_1_q), .Q(d_ff_2_q), .reset(RST));  // open: Qn, preset, en
  D_Flip_Flop #(.trigger("rising")) d_ff_3 (
    .clk(CLK_out), .D(d_ff_2_q), .Q(d_ff_3_q), .reset(RST));  // open: Qn, preset, en
  not not_1 (not_1_out, d_ff_2_q);
  and and_1 (Out, d_ff_3_q, not_1_out, d_ff_1_q);

  // Notes on the sheet:
  //   Mat: 405790
  //   Bruno Calil Nicoliello Moreira
endmodule
