// Logisim project Ex02.circ as structural Verilog: 1 circuit, main circuit main
module main (
  input  DATA,
  input  RST,
  output Out
);

  wire and_1_out, CLK_out, d_ff_1_q, d_ff_2_q, d_ff_3_q, d_ff_4_q, not_1_out, not_2_out;

  Clock #(.highDuration(1), .lowDuration(1)) CLK (.out(CLK_out));
  D_Flip_Flop #(.trigger("rising")) d_ff_1 (
    .clk(CLK_out), .D(DATA), .Q(d_ff_1_q), .reset(RST));  // open: Qn, preset, en
  D_Flip_Flop #(.trigger("rising")) d_ff_2 (
    .clk(CLK_out), .D(d_ff_1_q), .Q(d_ff_2_q), .reset(RST));  // open: Qn, preset, en
  D_Flip_Flop #(.trigger("rising")) d_ff_3 (
    .clk(CLK_out), .D(d_ff_2_q), .Q(d_ff_3_q), .reset(RST));  // open: Qn, preset, en
  D_Flip_Flop #(.trigger("rising")) d_ff_4 (
    .clk(CLK_out), .D(d_ff_3_q), .Q(d_ff_4_q), .reset(RST));  // open: Qn, preset, en
  not not_1 (not_1_out, d_ff_4_q);
  not not_2 (not_2_out, d_ff_2_q);
  D_Flip_Flop #(.trigger("rising")) d_ff_5 (
    .clk(CLK_out), .D(and_1_out), .Q(Out), .reset(RST));  // open: Qn, preset, en
  and and_1 (and_1_out, not_1_out, d_ff_3_q, not_2_out, d_ff_1_q);

  // Notes on the sheet:
  //   Mat: 405790
  //   Mat: 405790
  //   Mat: 405790
  //   Bruno Calil Nicoliello Moreira
  //   Bruno Calil Nicoliello Moreira
  //   Bruno Calil Nicoliello Moreira 
endmodule
