// Logisim project Circuitos.circ as structural Verilog: 5 circuits, main circuit numero_01
module numero_01 (
  input  DATA,
  input  Clear,
  output s
);

  wire CLK_out, d_ff_1_q, d_ff_2_q, d_ff_3_q, not_1_out;

  Clock #(.highDuration(1), .lowDuration(1)) CLK (.out(CLK_out));
  D_Flip_Flop #(.trigger("rising")) d_ff_1 (
    .clk(CLK_out), .D(DATA), .Q(d_ff_1_q), .reset(Clear));  // open: Qn, preset, en
  D_Flip_Flop #(.trigger("rising")) d_ff_2 (
    .clk(CLK_out), .D(d_ff_1_q), .Q(d_ff_2_q), .reset(Clear));  // open: Qn, preset, en
  D_Flip_Flop #(.trigger("rising")) d_ff_3 (
    .clk(CLK_out), .D(d_ff_2_q), .Q(d_ff_3_q), .reset(Clear));  // open: Qn, preset, en
  not not_1 (not_1_out, d_ff_2_q);
  and and_1 (s, d_ff_3_q, not_1_out, d_ff_1_q);

  // Notes on the sheet:
  //   RECONHECER A SEQUENCIA 101
endmodule

module numero_02 (
  input  DATA,
  input  Clear,
  output s
);

  wire and_1_out, CLK_out, d_ff_1_q, d_ff_1_qn, d_ff_2_q, d_ff_3_q, d_ff_3_qn, d_ff_4_q, d_ff_5_q, or_1_out;

  Clock #(.highDuration(1), .lowDuration(1)) CLK (.out(CLK_out));
  or or_1 (or_1_out, Clear, d_ff_5_q);
  D_Flip_Flop #(.trigger("rising")) d_ff_1 (
    .clk(CLK_out), .D(DATA), .Q(d_ff_1_q), .Qn(d_ff_1_qn), .reset(or_1_out));  // open: preset, en
  D_Flip_Flop #(.trigger("rising")) d_ff_2 (
    .clk(CLK_out), .D(d_ff_1_q), .Q(d_ff_2_q), .reset(or_1_out));  // open: Qn, preset, en
  D_Flip_Flop #(.trigger("rising")) d_ff_3 (
    .clk(CLK_out), .D(d_ff_2_q), .Q(d_ff_3_q), .Qn(d_ff_3_qn), .reset(or_1_out));  // open: preset, en
  and and_1 (and_1_out, d_ff_4_q, d_ff_3_qn, d_ff_2_q, d_ff_1_qn);
  D_Flip_Flop #(.trigger("rising")) d_ff_4 (
    .clk(CLK_out), .D(d_ff_3_q), .Q(d_ff_4_q), .reset(or_1_out));  // open: Qn, preset, en
  D_Flip_Flop #(.trigger("rising")) d_ff_5 (.clk(CLK_out), .D(and_1_out), .Q(d_ff_5_q));  // open: Qn, preset, en, reset
  D_Flip_Flop #(.trigger("rising")) d_ff_6 (.clk(CLK_out), .D(d_ff_5_q), .Q(s));  // open: Qn, preset, en, reset

  // Notes on the sheet:
  //   RECONHECER A SEQUENCIA 0101 SEM INTERSECAO
endmodule

module numero_03 (
  input  DATA,
  input  Clear,
  output s
);

  wire CLK_out, d_ff_1_q, d_ff_2_q, d_ff_3_q, d_ff_4_q, not_1_out, not_2_out;

  Clock #(.highDuration(1), .lowDuration(1)) CLK (.out(CLK_out));
  D_Flip_Flop #(.trigger("rising")) d_ff_1 (
    .clk(CLK_out), .D(DATA), .Q(d_ff_1_q), .reset(Clear));  // open: Qn, preset, en
  D_Flip_Flop #(.trigger("rising")) d_ff_2 (
    .clk(CLK_out), .D(d_ff_1_q), .Q(d_ff_2_q), .reset(Clear));  // open: Qn, preset, en
  D_Flip_Flop #(.trigger("rising")) d_ff_3 (
    .clk(CLK_out), .D(d_ff_2_q), .Q(d_ff_3_q), .reset(Clear));  // open: Qn, preset, en
  not not_1 (not_1_out, d_ff_3_q);
  not not_2 (not_2_out, d_ff_2_q);
  D_Flip_Flop #(.trigger("rising")) d_ff_4 (
    .clk(CLK_out), .D(d_ff_3_q), .Q(d_ff_4_q), .reset(Clear));  // open: Qn, preset, en
  and and_1 (s, d_ff_4_q, not_1_out, not_2_out, d_ff_1_q);

  // Notes on the sheet:
  //   RECONHECER A SEQUENCIA 1001
endmodule

module numero_04 (
  input  DATA,
  input  Clear,
  output s
);

  wire and_1_out, and_2_out, CLK_out, d_ff_1_q, d_ff_2_q, d_ff_3_q, not_1_out, not_2_out, not_3_out;

  Clock #(.highDuration(1), .lowDuration(1)) CLK (.out(CLK_out));
  D_Flip_Flop #(.trigger("rising")) d_ff_1 (
    .clk(CLK_out), .D(DATA), .Q(d_ff_1_q), .reset(Clear));  // open: Qn, preset, en
  D_Flip_Flop #(.trigger("rising")) d_ff_2 (
    .clk(CLK_out), .D(d_ff_1_q), .Q(d_ff_2_q), .reset(Clear));  // open: Qn, preset, en
  not not_1 (not_1_out, d_ff_2_q);
  D_Flip_Flop #(.trigger("rising")) d_ff_3 (
    .clk(CLK_out), .D(d_ff_2_q), .Q(d_ff_3_q), .reset(Clear));  // open: Qn, preset, en
  and and_1 (and_1_out, d_ff_3_q, not_1_out, d_ff_1_q);
  not not_2 (not_2_out, d_ff_3_q);
  and and_2 (and_2_out, not_2_out, d_ff_2_q, not_3_out);
  not not_3 (not_3_out, d_ff_1_q);
  or or_1 (s, and_2_out, and_1_out);

  // Notes on the sheet:
  //   RECONHECER AS SEQUENCIAS 101 OU 010
endmodule

module numero_05 (
  input  DATA,
  input  Clear,
  output s
);

  wire and_1_out, and_2_out, CLK_out, d_ff_1_q, d_ff_2_q, d_ff_3_q, not_1_out, not_2_out, not_3_out;

  Clock #(.highDuration(1), .lowDuration(1)) CLK (.out(CLK_out));
  D_Flip_Flop #(.trigger("rising")) d_ff_1 (
    .clk(CLK_out), .D(DATA), .Q(d_ff_1_q), .reset(Clear));  // open: Qn, preset, en
  D_Flip_Flop #(.trigger("rising")) d_ff_2 (
    .clk(CLK_out), .D(d_ff_1_q), .Q(d_ff_2_q), .reset(Clear));  // open: Qn, preset, en
  D_Flip_Flop #(.trigger("rising")) d_ff_3 (
    .clk(CLK_out), .D(d_ff_2_q), .Q(d_ff_3_q), .reset(Clear));  // open: Qn, preset, en
  and and_1 (and_1_out, d_ff_3_q, d_ff_2_q, d_ff_1_q);
  not not_1 (not_1_out, d_ff_3_q);
  not not_2 (not_2_out, d_ff_2_q);
  and and_2 (and_2_out, not_1_out, not_2_out, not_3_out);
  not not_3 (not_3_out, d_ff_1_q);
  or or_1 (s, and_2_out, and_1_out);

  // Notes on the sheet:
  //   RECONHECER AS SEQUENCIAS 000 OU 111
endmodule
