// Logisim project implementacao02.circ as structural Verilog: 1 circuit, main circuit main
module main (
  input  Entrada,
  input  Clear,
  output Encontrado_0101
);

  wire and_1_out, Clock_out, d_ff_1_q, d_ff_1_qn, d_ff_2_q, d_ff_3_q, d_ff_3_qn, d_ff_4_q;

  Clock #(.highDuration(1), .lowDuration(1)) Clock (.out(Clock_out));
  D_Flip_Flop #(.trigger("rising")) d_ff_1 (
    .clk(Clock_out), .D(Entrada), .Q(d_ff_1_q), .Qn(d_ff_1_qn), .reset(Clear));  // open: preset, en
  D_Flip_Flop #(.trigger("rising")) d_ff_2 (
    .clk(Clock_out), .D(d_ff_1_q), .Q(d_ff_2_q), .reset(Clear));  // open: Qn, preset, en
  D_Flip_Flop #(.trigger("rising")) d_ff_3 (
    .clk(Clock_out), .D(d_ff_2_q), .Q(d_ff_3_q), .Qn(d_ff_3_qn), .reset(Clear));  // open: preset, en
  D_Flip_Flop #(.trigger("rising")) d_ff_4 (
    .clk(Clock_out), .D(d_ff_3_q), .Q(d_ff_4_q), .reset(Clear));  // open: Qn, preset, en
  and and_1 (and_1_out, d_ff_4_q, d_ff_3_qn, d_ff_2_q, d_ff_1_qn);
  D_Flip_Flop #(.trigger("rising")) d_ff_5 (
    .clk(Clock_out), .D(and_1_out), .Q(Encontrado_0101), .reset(Clear));  // open: Qn, preset, en

  // Notes on the sheet:
  //   Arquitetura de Computadores - Guia 11
  //   Implementação 02
  //   Máquina de Estados Finitos que reconhece a sequencia 0101
  //   Tiago Menegaz de Melo Garcia         405844
endmodule
