// Logisim project implementacao03.circ as structural Verilog: 1 circuit, main circuit main
module main (
  input  Dado,
  input  Reset,
  output Encontrado_1001
);

  wire Clock_out, d_ff_1_q, d_ff_2_q, d_ff_2_qn, d_ff_3_q, d_ff_3_qn, d_ff_4_q;

  Clock #(.highDuration(1), .lowDuration(1)) Clock (.out(Clock_out));
  D_Flip_Flop #(.trigger("rising")) d_ff_1 (
    .clk(Clock_out), .D(Dado), .Q(d_ff_1_q), .reset(Reset));  // open: Qn, preset, en
  D_Flip_Flop #(.trigger("rising")) d_ff_2 (
    .clk(Clock_out), .D(d_ff_1_q), .Q(d_ff_2_q), .Qn(d_ff_2_qn), .reset(Reset));  // open: preset, en
  D_Flip_Flop #(.trigger("rising")) d_ff_3 (
    .clk(Clock_out), .D(d_ff_2_q), .Q(d_ff_3_q), .Qn(d_ff_3_qn), .reset(Reset));  // open: preset, en
  D_Flip_Flop #(.trigger("rising")) d_ff_4 (
    .clk(Clock_out), .D(d_ff_3_q), .Q(d_ff_4_q));  // open: Qn, preset, en, reset
  and and_1 (Encontrado_1001, d_ff_4_q, d_ff_3_qn, d_ff_2_qn, d_ff_1_q);

  // Notes on the sheet:
  //   Arquitetura de Computadores - Guia 11
  //   Implementação 03
  //   Máquina de Estados Finitos que reconhece a sequencia 1001
  //   Tiago Menegaz de Melo Garcia           405844
endmodule
