// Logisim project implementacao05.circ as structural Verilog: 1 circuit, main circuit main
module main (
  input  Dado,
  input  Reset,
  output Encontrado_111_ou_000
);

  wire and_1_out, and_2_out, Clock_out, d_ff_1_q, d_ff_1_qn, d_ff_2_q, d_ff_2_qn, d_ff_3_q, d_ff_3_qn;

  Clock #(.highDuration(1), .lowDuration(1)) Clock (.out(Clock_out));
  D_Flip_Flop #(.trigger("rising")) d_ff_1 (
    .clk(Clock_out), .D(Dado), .Q(d_ff_1_q), .Qn(d_ff_1_qn), .reset(Reset));  // open: preset, en
  D_Flip_Flop #(.trigger("rising")) d_ff_2 (
    .clk(Clock_out), .D(d_ff_1_q), .Q(d_ff_2_q), .Qn(d_ff_2_qn), .reset(Reset));  // open: preset, en
  D_Flip_Flop #(.trigger("rising")) d_ff_3 (
    .clk(Clock_out), .D(d_ff_2_q), .Q(d_ff_3_q), .Qn(d_ff_3_qn), .reset(Reset));  // open: preset, en
  and and_1 (and_1_out, d_ff_3_q, d_ff_2_q, d_ff_1_q);
  and and_2 (and_2_out, d_ff_3_qn, d_ff_2_qn, d_ff_1_qn);
  or or_1 (Encontrado_111_ou_000, and_1_out, and_2_out);

  // Notes on the sheet:
  //   Arquitetura de Computadores - Guia 11
  //   Implementação 04
  //   Máquina de Estados Finitos que reconhece a sequencia 111 ou 000
  //   Tiago Menegaz de Melo Garcia           405844
endmodule
