// Logisim project guia11 - 412727.circ as structural Verilog: 6 circuits, main circuit main
module main (
  input  d,
  input  clk,
  input  clr,
  output ex1,
  output ex2,
  output ex3,
  output ex4,
  output ex5
);

  Exercicio_1 exercicio_1_1 (.d(d), .cl(clr), .out_10(ex1));  // open: out_3, out_4, out_5, out_6, out_7, out_8, out_9
  Exercicio_2 exercicio_2_1 (.d(d), .cl(clr), .out_10(ex2));  // open: out_3, out_4, out_5, out_6, out_7, out_8, out_9
  Exercicio_3 exercicio_3_1 (.d(d), .cl(clr), .out_10(ex3));  // open: out_3, out_4, out_5, out_6, out_7, out_8, out_9
  Exercicio_4 exercicio_4_1 (
    .d(d), .cl(clr), .\_0__não (ex4));  // open: out_3, out_4, out_5, out_6, out_7, out_8, out_9
  Exercicio_5 exercicio_5_1 (
    .d(d), .cl(clr), .\_0__não (ex5));  // open: out_3, out_4, out_5, out_6, out_7, out_8, out_9

  // Notes on the sheet:
  //   AUGUSTO FERREIRA ANDRADE DO CARMO - 412727
  //   Theldo, não sei por que, mas a entrade não está aparecendo aqui, então tem que ir olhando de cricuito em circuito
endmodule

module Exercicio_1 (
  input  d,
  input  cl,
  output out_3,
  output out_4,
  output out_5,
  output out_6,
  output out_7,
  output out_8,
  output out_9,
  output out_10
);

  wire and_1_out, and_2_out, and_3_out, and_4_out, and_5_out, and_6_out, and_7_out, clk_out, not_1_out,
       not_2_out, not_3_out, not_4_out, not_5_out, not_6_out, not_7_out;

  Clock clk (.out(clk_out));
  D_Flip_Flop d_ff_1 (.clk(clk_out), .D(d), .Q(out_9), .reset(cl));  // open: Qn, preset, en
  D_Flip_Flop d_ff_2 (.clk(clk_out), .D(out_9), .Q(out_8), .reset(cl));  // open: Qn, preset, en
  not not_1 (not_1_out, out_9);
  not not_2 (not_2_out, out_8);
  D_Flip_Flop d_ff_3 (.clk(clk_out), .D(out_8), .Q(out_7), .reset(cl));  // open: Qn, preset, en
  not not_3 (not_3_out, out_7);
  D_Flip_Flop d_ff_4 (.clk(clk_out), .D(out_7), .Q(out_6), .reset(cl));  // open: Qn, preset, en
  not not_4 (not_4_out, out_6);
  D_Flip_Flop d_ff_5 (.clk(clk_out), .D(out_6), .Q(out_5), .reset(cl));  // open: Qn, preset, en
  not not_5 (not_5_out, out_5);
  D_Flip_Flop d_ff_6 (.clk(clk_out), .D(out_4), .Q(out_3));  // open: Qn, preset, en, reset
  D_Flip_Flop d_ff_7 (.clk(clk_out), .D(out_5), .Q(out_4), .reset(cl));  // open: Qn, preset, en
  not not_6 (not_6_out, out_4);
  not not_7 (not_7_out, out_3);
  and and_1 (and_1_out, out_9, not_2_out, out_7);
  and and_2 (and_2_out, out_8, not_3_out, out_6);
  and and_3 (and_3_out, out_7, not_4_out, out_5);
  and and_4 (and_4_out, out_6, not_5_out, out_4);
  and and_5 (and_5_out, out_5, not_6_out, out_3);
  and and_6 (and_6_out, out_4, not_7_out, out_9);
  and and_7 (and_7_out, out_3, not_1_out, out_8);
  or or_1 (out_10, and_1_out, and_2_out, and_3_out, and_4_out, and_5_out, and_6_out, and_7_out);

  // Notes on the sheet:
  //   (1) sim
  //   (0) não
  //   Possui a sequencia?
endmodule

module Exercicio_2 (
  input  d,
  input  cl,
  output out_3,
  output out_4,
  output out_5,
  output out_6,
  output out_7,
  output out_8,
  output out_9,
  output out_10
);

  wire and_1_out, and_2_out, and_3_out, and_4_out, and_5_out, and_6_out, and_7_out, and_8_out, and_9_out,
       and_10_out, and_11_out, and_12_out, and_13_out, and_14_out, and_15_out, clk_out, not_1_out, not_2_out,
       not_3_out, not_4_out, not_5_out, not_6_out, not_7_out, not_8_out, not_9_out, not_10_out, not_11_out,
       not_12_out, not_13_out, not_14_out, or_1_out;

  Clock clk (.out(clk_out));
  D_Flip_Flop d_ff_1 (.clk(clk_out), .D(d), .Q(out_9), .reset(cl));  // open: Qn, preset, en
  D_Flip_Flop d_ff_2 (.clk(clk_out), .D(out_9), .Q(out_8), .reset(cl));  // open: Qn, preset, en
  not not_1 (not_1_out, out_8);
  not not_2 (not_2_out, out_9);
  D_Flip_Flop d_ff_3 (.clk(clk_out), .D(out_8), .Q(out_7), .reset(cl));  // open: Qn, preset, en
  not not_3 (not_3_out, out_7);
  D_Flip_Flop d_ff_4 (.clk(clk_out), .D(out_7), .Q(out_6), .reset(cl));  // open: Qn, preset, en
  not not_4 (not_4_out, out_6);
  D_Flip_Flop d_ff_5 (.clk(clk_out), .D(out_6), .Q(out_5), .reset(cl));  // open: Qn, preset, en
  not not_5 (not_5_out, out_5);
  D_Flip_Flop d_ff_6 (.clk(clk_out), .D(out_5), .Q(out_4), .reset(cl));  // open: Qn, preset, en
  D_Flip_Flop d_ff_7 (.clk(clk_out), .D(out_4), .Q(out_3));  // open: Qn, preset, en, reset
  not not_6 (not_6_out, out_4);
  not not_7 (not_7_out, out_3);
  and and_1 (and_1_out, not_2_out, out_8, not_3_out, out_6);
  and and_2 (and_2_out, not_1_out, out_7, not_4_out, out_5);
  and and_3 (and_3_out, not_3_out, out_6, not_5_out, out_4);
  and and_4 (and_4_out, not_4_out, out_5, not_6_out, out_3);
  and and_5 (and_5_out, not_5_out, out_4, not_7_out, out_9);
  and and_6 (and_6_out, not_6_out, out_3, not_2_out, out_8);
  and and_7 (and_7_out, not_7_out, out_9, not_1_out, out_7);
  and and_8 (and_8_out, not_2_out, out_8, not_3_out, out_6, not_5_out, out_4);
  not not_8 (not_8_out, and_8_out);
  and and_9 (and_9_out, not_1_out, out_7, not_4_out, out_5, not_6_out, out_3);
  not not_9 (not_9_out, and_9_out);
  not not_10 (not_10_out, and_10_out);
  and and_10 (and_10_out, not_3_out, out_6, not_5_out, out_4, not_7_out, out_9);
  not not_11 (not_11_out, and_11_out);
  and and_11 (and_11_out, not_4_out, out_5, not_6_out, out_3, not_2_out, out_8);
  and and_12 (and_12_out, not_5_out, out_4, not_7_out, out_9, not_1_out, out_7);
  not not_12 (not_12_out, and_12_out);
  not not_13 (not_13_out, and_13_out);
  and and_13 (and_13_out, not_6_out, out_3, not_2_out, out_8, not_3_out, out_6);
  and and_14 (and_14_out, not_7_out, out_9, not_1_out, out_7, not_4_out, out_5);
  not not_14 (not_14_out, and_14_out);
  or or_1 (or_1_out, and_1_out, and_2_out, and_3_out, and_4_out, and_5_out, and_6_out, and_7_out);
  and and_15 (and_15_out, or_1_out, not_8_out, not_9_out, not_10_out, not_11_out, not_12_out, not_13_out, not_14_out);
  D_Flip_Flop d_ff_8 (.clk(clk_out), .D(and_15_out), .Q(out_10));  // open: Qn, preset, en, reset

  // Notes on the sheet:
  //   Possui a sequencia?
  //   (1) sim
  //   (0) não
endmodule

module Exercicio_3 (
  input  d,
  input  cl,
  output out_3,
  output out_4,
  output out_5,
  output out_6,
  output out_7,
  output out_8,
  output out_9,
  output out_10
);

  wire and_1_out, and_2_out, and_3_out, and_4_out, and_5_out, and_6_out, and_7_out, clk_out, not_1_out,
       not_2_out, not_3_out, not_4_out, not_5_out, not_6_out, not_7_out;

  Clock clk (.out(clk_out));
  D_Flip_Flop d_ff_1 (.clk(clk_out), .D(d), .Q(out_9), .reset(cl));  // open: Qn, preset, en
  D_Flip_Flop d_ff_2 (.clk(clk_out), .D(out_9), .Q(out_8), .reset(cl));  // open: Qn, preset, en
  not not_1 (not_1_out, out_8);
  not not_2 (not_2_out, out_9);
  D_Flip_Flop d_ff_3 (.clk(clk_out), .D(out_8), .Q(out_7), .reset(cl));  // open: Qn, preset, en
  not not_3 (not_3_out, out_7);
  D_Flip_Flop d_ff_4 (.clk(clk_out), .D(out_7), .Q(out_6), .reset(cl));  // open: Qn, preset, en
  not not_4 (not_4_out, out_6);
  D_Flip_Flop d_ff_5 (.clk(clk_out), .D(out_6), .Q(out_5), .reset(cl));  // open: Qn, preset, en
  not not_5 (not_5_out, out_5);
  D_Flip_Flop d_ff_6 (.clk(clk_out), .D(out_5), .Q(out_4), .reset(cl));  // open: Qn, preset, en
  D_Flip_Flop d_ff_7 (.clk(clk_out), .D(out_4), .Q(out_3));  // open: Qn, preset, en, reset
  not not_6 (not_6_out, out_4);
  not not_7 (not_7_out, out_3);
  and and_1 (and_1_out, out_9, not_1_out, not_3_out, out_6);
  and and_2 (and_2_out, out_8, not_3_out, not_4_out, out_5);
  and and_3 (and_3_out, out_7, not_4_out, not_5_out, out_4);
  and and_4 (and_4_out, out_6, not_5_out, not_6_out, out_3);
  and and_5 (and_5_out, out_5, not_6_out, not_7_out, out_9);
  and and_6 (and_6_out, out_4, not_7_out, not_2_out, out_8);
  and and_7 (and_7_out, out_3, not_2_out, not_1_out, out_7);
  or or_1 (out_10, and_1_out, and_2_out, and_3_out, and_4_out, and_5_out, and_6_out, and_7_out);

  // Notes on the sheet:
  //   (1) sim
  //   (0) não
  //   Possui a sequencia?
endmodule

module Exercicio_4 (
  input  d,
  input  cl,
  output out_3,
  output out_4,
  output out_5,
  output out_6,
  output out_7,
  output out_8,
  output out_9,
  output \_0__não 
);

  wire and_1_out, clk_out, nor_1_out;

  Clock clk (.out(clk_out));
  D_Flip_Flop d_ff_1 (.clk(clk_out), .D(d), .Q(out_9), .reset(cl));  // open: Qn, preset, en
  D_Flip_Flop d_ff_2 (.clk(clk_out), .D(out_9), .Q(out_8), .reset(cl));  // open: Qn, preset, en
  D_Flip_Flop d_ff_3 (.clk(clk_out), .D(out_8), .Q(out_7), .reset(cl));  // open: Qn, preset, en
  D_Flip_Flop d_ff_4 (.clk(clk_out), .D(out_7), .Q(out_6), .reset(cl));  // open: Qn, preset, en
  D_Flip_Flop d_ff_5 (.clk(clk_out), .D(out_6), .Q(out_5), .reset(cl));  // open: Qn, preset, en
  D_Flip_Flop d_ff_6 (.clk(clk_out), .D(out_5), .Q(out_4), .reset(cl));  // open: Qn, preset, en
  D_Flip_Flop d_ff_7 (.clk(clk_out), .D(out_4), .Q(out_3));  // open: Qn, preset, en, reset
  and and_1 (and_1_out, out_3, out_4, out_5, out_6, out_7, out_8, out_9);
  nor nor_1 (nor_1_out, out_3, out_4, out_4, out_5, out_6, out_8, out_9);
  nor nor_2 (\_0__não , and_1_out, nor_1_out);

  // Notes on the sheet:
  //   (1) sim
  //   Possui a sequencia?
  //   Possui a sequencia?
endmodule

module Exercicio_5 (
  input  d,
  input  cl,
  output out_3,
  output out_4,
  output out_5,
  output out_6,
  output out_7,
  output out_8,
  output out_9,
  output \_0__não 
);

  wire and_1_out, and_2_out, and_3_out, and_4_out, and_5_out, and_6_out, and_7_out, and_8_out, and_9_out,
       and_10_out, and_11_out, and_12_out, and_13_out, and_14_out, clk_out, not_1_out, not_2_out, not_3_out,
       not_4_out, not_5_out, not_6_out, not_7_out, or_1_out, or_2_out;

  Clock clk (.out(clk_out));
  D_Flip_Flop d_ff_1 (.clk(clk_out), .D(d), .Q(out_9), .reset(cl));  // open: Qn, preset, en
  D_Flip_Flop d_ff_2 (.clk(clk_out), .D(out_9), .Q(out_8), .reset(cl));  // open: Qn, preset, en
  not not_1 (not_1_out, out_9);
  not not_2 (not_2_out, out_8);
  D_Flip_Flop d_ff_3 (.clk(clk_out), .D(out_8), .Q(out_7), .reset(cl));  // open: Qn, preset, en
  not not_3 (not_3_out, out_7);
  D_Flip_Flop d_ff_4 (.clk(clk_out), .D(out_7), .Q(out_6), .reset(cl));  // open: Qn, preset, en
  not not_4 (not_4_out, out_6);
  D_Flip_Flop d_ff_5 (.clk(clk_out), .D(out_6), .Q(out_5), .reset(cl));  // open: Qn, preset, en
  not not_5 (not_5_out, out_5);
  D_Flip_Flop d_ff_6 (.clk(clk_out), .D(out_5), .Q(out_4), .reset(cl));  // open: Qn, preset, en
  D_Flip_Flop d_ff_7 (.clk(clk_out), .D(out_4), .Q(out_3));  // open: Qn, preset, en, reset
  not not_6 (not_6_out, out_4);
  not not_7 (not_7_out, out_3);
  and and_1 (and_1_out, out_9, out_8, out_7);
  and and_2 (and_2_out, out_8, out_7, out_6);
  and and_3 (and_3_out, out_7, out_6, out_5);
  and and_4 (and_4_out, out_6, out_5, out_4);
  and and_5 (and_5_out, out_5, out_4, out_3);
  and and_6 (and_6_out, out_4, out_3, out_9);
  and and_7 (and_7_out, out_3, out_9, out_8);
  and and_8 (and_8_out, not_1_out, not_2_out, not_3_out);
  and and_9 (and_9_out, not_2_out, not_3_out, not_4_out);
  and and_10 (and_10_out, not_3_out, not_4_out, not_5_out);
  and and_11 (and_11_out, not_4_out, not_5_out, not_6_out);
  and and_12 (and_12_out, not_5_out, not_6_out, not_7_out);
  and and_13 (and_13_out, not_6_out, not_7_out, not_1_out);
  and and_14 (and_14_out, not_7_out, not_1_out, not_2_out);
  or or_1 (or_1_out, and_1_out, and_2_out, and_3_out, and_4_out, and_5_out, and_6_out, and_7_out);
  or or_2 (or_2_out, and_8_out, and_9_out, and_10_out, and_11_out, and_12_out, and_13_out, and_14_out);
  or or_3 (\_0__não , or_1_out, or_2_out);

  // Notes on the sheet:
  //   Possui a sequencia?
  //   (1) sim
endmodule
