// Logisim project Guia11.circ as structural Verilog: 6 circuits, main circuit main
module main (
);


  // Notes on the sheet:
  //   Lucas Teixeira Santos - 415383
endmodule

module Ex01 (
  input  DATA,
  input  RST,
  output s
);

  wire and_1_out, and_2_out, and_3_out, CLK_out, d_ff_1_q, d_ff_2_q, d_ff_2_qn, d_ff_3_q, d_ff_3_qn,
       d_ff_4_q, d_ff_4_qn, d_ff_5_q;

  Clock #(.highDuration(1), .lowDuration(1)) CLK (.out(CLK_out));
  D_Flip_Flop #(.trigger("rising")) d_ff_1 (
    .clk(CLK_out), .D(DATA), .Q(d_ff_1_q), .reset(RST));  // open: Qn, preset, en
  and and_1 (and_1_out, d_ff_1_q, d_ff_2_qn, d_ff_3_q);
  D_Flip_Flop #(.trigger("rising")) d_ff_2 (
    .clk(CLK_out), .D(d_ff_1_q), .Q(d_ff_2_q), .Qn(d_ff_2_qn), .reset(RST));  // open: preset, en
  and and_2 (and_2_out, d_ff_2_q, d_ff_3_qn, d_ff_4_q);
  D_Flip_Flop #(.trigger("rising")) d_ff_3 (
    .clk(CLK_out), .D(d_ff_2_q), .Q(d_ff_3_q), .Qn(d_ff_3_qn), .reset(RST));  // open: preset, en
  D_Flip_Flop #(.trigger("rising")) d_ff_4 (
    .clk(CLK_out), .D(d_ff_3_q), .Q(d_ff_4_q), .Qn(d_ff_4_qn), .reset(RST));  // open: preset, en
  and and_3 (and_3_out, d_ff_3_q, d_ff_4_qn, d_ff_5_q);
  D_Flip_Flop #(.trigger("rising")) d_ff_5 (
    .clk(CLK_out), .D(d_ff_4_q), .Q(d_ff_5_q), .reset(RST));  // open: Qn, preset, en
  or or_1 (s, and_3_out, and_2_out, and_1_out);

  // Notes on the sheet:
  //   101
endmodule

module Ex03 (
  input  DATA,
  input  RST,
  output s
);

  wire and_1_out, and_2_out, and_3_out, and_4_out, CLK_out, d_ff_1_q, d_ff_2_q, d_ff_2_qn, d_ff_3_q,
       d_ff_3_qn, d_ff_4_q, d_ff_4_qn, d_ff_5_q, d_ff_5_qn, d_ff_6_q, d_ff_6_qn, d_ff_7_q;

  Clock #(.highDuration(1), .lowDuration(1)) CLK (.out(CLK_out));
  D_Flip_Flop #(.trigger("rising")) d_ff_1 (
    .clk(CLK_out), .D(DATA), .Q(d_ff_1_q), .reset(RST));  // open: Qn, preset, en
  D_Flip_Flop #(.trigger("rising")) d_ff_2 (
    .clk(CLK_out), .D(d_ff_1_q), .Q(d_ff_2_q), .Qn(d_ff_2_qn), .reset(RST));  // open: preset, en
  and and_1 (and_1_out, d_ff_1_q, d_ff_2_qn, d_ff_3_qn, d_ff_4_q);
  D_Flip_Flop #(.trigger("rising")) d_ff_3 (
    .clk(CLK_out), .D(d_ff_2_q), .Q(d_ff_3_q), .Qn(d_ff_3_qn), .reset(RST));  // open: preset, en
  and and_2 (and_2_out, d_ff_2_q, d_ff_3_qn, d_ff_4_qn, d_ff_5_q);
  D_Flip_Flop #(.trigger("rising")) d_ff_4 (
    .clk(CLK_out), .D(d_ff_3_q), .Q(d_ff_4_q), .Qn(d_ff_4_qn), .reset(RST));  // open: preset, en
  and and_3 (and_3_out, d_ff_3_q, d_ff_4_qn, d_ff_5_qn, d_ff_6_q);
  D_Flip_Flop #(.trigger("rising")) d_ff_5 (
    .clk(CLK_out), .D(d_ff_4_q), .Q(d_ff_5_q), .Qn(d_ff_5_qn), .reset(RST));  // open: preset, en
  and and_4 (and_4_out, d_ff_4_q, d_ff_5_qn, d_ff_6_qn, d_ff_7_q);
  D_Flip_Flop #(.trigger("rising")) d_ff_6 (
    .clk(CLK_out), .D(d_ff_5_q), .Q(d_ff_6_q), .Qn(d_ff_6_qn), .reset(RST));  // open: preset, en
  or or_1 (s, and_4_out, and_3_out, and_2_out, and_1_out);
  D_Flip_Flop #(.trigger("rising")) d_ff_7 (
    .clk(CLK_out), .D(d_ff_6_q), .Q(d_ff_7_q), .reset(RST));  // open: Qn, preset, en

  // Notes on the sheet:
  //   1001
endmodule

module Ex04 (
  input  DATA,
  input  RST,
  output s
);

  wire and_1_out, and_2_out, and_3_out, and_4_out, and_5_out, and_6_out, CLK_out, d_ff_1_q, d_ff_1_qn,
       d_ff_2_q, d_ff_2_qn, d_ff_3_q, d_ff_3_qn, d_ff_4_q, d_ff_4_qn, d_ff_5_q, d_ff_5_qn, or_1_out,
       or_2_out, or_3_out;

  Clock #(.highDuration(1), .lowDuration(1)) CLK (.out(CLK_out));
  D_Flip_Flop #(.trigger("rising")) d_ff_1 (
    .clk(CLK_out), .D(DATA), .Q(d_ff_1_q), .Qn(d_ff_1_qn), .reset(RST));  // open: preset, en
  and and_1 (and_1_out, d_ff_1_qn, d_ff_2_q, d_ff_3_qn);
  D_Flip_Flop #(.trigger("rising")) d_ff_2 (
    .clk(CLK_out), .D(d_ff_1_q), .Q(d_ff_2_q), .Qn(d_ff_2_qn), .reset(RST));  // open: preset, en
  and and_2 (and_2_out, d_ff_1_q, d_ff_2_qn, d_ff_3_q);
  or or_1 (or_1_out, and_1_out, and_2_out);
  D_Flip_Flop #(.trigger("rising")) d_ff_3 (
    .clk(CLK_out), .D(d_ff_2_q), .Q(d_ff_3_q), .Qn(d_ff_3_qn), .reset(RST));  // open: preset, en
  and and_3 (and_3_out, d_ff_2_qn, d_ff_3_q, d_ff_4_qn);
  and and_4 (and_4_out, d_ff_2_q, d_ff_3_qn, d_ff_4_q);
  or or_2 (or_2_out, and_3_out, and_4_out);
  D_Flip_Flop #(.trigger("rising")) d_ff_4 (
    .clk(CLK_out), .D(d_ff_3_q), .Q(d_ff_4_q), .Qn(d_ff_4_qn), .reset(RST));  // open: preset, en
  and and_5 (and_5_out, d_ff_3_qn, d_ff_4_q, d_ff_5_qn);
  D_Flip_Flop #(.trigger("rising")) d_ff_5 (
    .clk(CLK_out), .D(d_ff_4_q), .Q(d_ff_5_q), .Qn(d_ff_5_qn), .reset(RST));  // open: preset, en
  and and_6 (and_6_out, d_ff_3_q, d_ff_4_qn, d_ff_5_q);
  or or_3 (or_3_out, and_5_out, and_6_out);
  or or_4 (s, or_3_out, or_2_out, or_1_out);

  // Notes on the sheet:
  //   010 ou 101
endmodule

module Ex05 (
  input  DATA,
  input  RST,
  output s
);

  wire and_1_out, and_2_out, and_3_out, and_4_out, and_5_out, and_6_out, CLK_out, d_ff_1_q, d_ff_1_qn,
       d_ff_2_q, d_ff_2_qn, d_ff_3_q, d_ff_3_qn, d_ff_4_q, d_ff_4_qn, d_ff_5_q, d_ff_5_qn, or_1_out,
       or_2_out, or_3_out;

  Clock #(.highDuration(1), .lowDuration(1)) CLK (.out(CLK_out));
  and and_1 (and_1_out, d_ff_1_qn, d_ff_2_qn, d_ff_3_qn);
  D_Flip_Flop #(.trigger("rising")) d_ff_1 (
    .clk(CLK_out), .D(DATA), .Q(d_ff_1_q), .Qn(d_ff_1_qn), .reset(RST));  // open: preset, en
  and and_2 (and_2_out, d_ff_1_q, d_ff_2_q, d_ff_3_q);
  or or_1 (or_1_out, and_1_out, and_2_out);
  D_Flip_Flop #(.trigger("rising")) d_ff_2 (
    .clk(CLK_out), .D(d_ff_1_q), .Q(d_ff_2_q), .Qn(d_ff_2_qn), .reset(RST));  // open: preset, en
  and and_3 (and_3_out, d_ff_2_qn, d_ff_3_qn, d_ff_4_qn);
  D_Flip_Flop #(.trigger("rising")) d_ff_3 (
    .clk(CLK_out), .D(d_ff_2_q), .Q(d_ff_3_q), .Qn(d_ff_3_qn), .reset(RST));  // open: preset, en
  and and_4 (and_4_out, d_ff_2_q, d_ff_3_q, d_ff_4_q);
  or or_2 (or_2_out, and_3_out, and_4_out);
  D_Flip_Flop #(.trigger("rising")) d_ff_4 (
    .clk(CLK_out), .D(d_ff_3_q), .Q(d_ff_4_q), .Qn(d_ff_4_qn), .reset(RST));  // open: preset, en
  and and_5 (and_5_out, d_ff_3_qn, d_ff_4_qn, d_ff_5_qn);
  D_Flip_Flop #(.trigger("rising")) d_ff_5 (
    .clk(CLK_out), .D(d_ff_4_q), .Q(d_ff_5_q), .Qn(d_ff_5_qn), .reset(RST));  // open: preset, en
  and and_6 (and_6_out, d_ff_3_q, d_ff_4_q, d_ff_5_q);
  or or_3 (or_3_out, and_5_out, and_6_out);
  or or_4 (s, or_3_out, or_2_out, or_1_out);

  // Notes on the sheet:
  //   000 ou 111
endmodule

module Ex02 (
  input  DATA,
  input  RST
);

  wire and_1_out, and_2_out, and_3_out, CLK_out, d_ff_1_q, d_ff_1_qn, d_ff_2_q, d_ff_2_qn, d_ff_3_q,
       d_ff_3_qn, d_ff_4_q, d_ff_4_qn, d_ff_5_q, d_ff_5_qn, d_ff_6_q, or_1_out, xor_1_out;

  Clock #(.highDuration(1), .lowDuration(1)) CLK (.out(CLK_out));
  D_Flip_Flop #(.trigger("rising")) d_ff_1 (
    .clk(CLK_out), .D(DATA), .Q(d_ff_1_q), .Qn(d_ff_1_qn), .reset(RST));  // open: preset, en
  D_Flip_Flop #(.trigger("rising")) d_ff_2 (
    .clk(CLK_out), .D(d_ff_1_q), .Q(d_ff_2_q), .Qn(d_ff_2_qn), .reset(RST));  // open: preset, en
  D_Flip_Flop #(.trigger("rising")) d_ff_3 (
    .clk(CLK_out), .D(d_ff_2_q), .Q(d_ff_3_q), .Qn(d_ff_3_qn), .reset(RST));  // open: preset, en
  D_Flip_Flop #(.trigger("rising")) d_ff_4 (
    .clk(CLK_out), .D(d_ff_3_q), .Q(d_ff_4_q), .Qn(d_ff_4_qn), .reset(RST));  // open: preset, en
  D_Flip_Flop #(.trigger("rising")) d_ff_5 (
    .clk(CLK_out), .D(d_ff_4_q), .Q(d_ff_5_q), .Qn(d_ff_5_qn), .reset(RST));  // open: preset, en
  and and_1 (and_1_out, d_ff_4_q, d_ff_3_qn, d_ff_2_q, d_ff_1_qn);
  D_Flip_Flop #(.trigger("rising")) d_ff_6 (
    .clk(CLK_out), .D(d_ff_5_q), .Q(d_ff_6_q), .reset(RST));  // open: Qn, preset, en
  and and_2 (and_2_out, d_ff_5_q, d_ff_4_qn, d_ff_3_q, d_ff_2_qn);
  or or_1 (or_1_out, and_2_out, xor_1_out);
  and and_3 (and_3_out, d_ff_6_q, d_ff_5_qn, d_ff_4_q, d_ff_3_qn);
  D_Flip_Flop #(.trigger("rising")) d_ff_7 (.clk(CLK_out), .D(or_1_out), .reset(RST));  // open: Q, Qn, preset, en
  xor xor_1 (xor_1_out, and_3_out, and_1_out);

  // Notes on the sheet:
  //   0101
  //   desconsiderando 010101 com a porta XOR
endmodule
