// Logisim project celso.circ as structural Verilog: 5 circuits, main circuit main
module main (
  input  DATA,
  input  RST,
  output out_3
);

  wire CLK_out, d_ff_1_q, d_ff_2_q, d_ff_3_q, not_1_out;

  Clock #(.highDuration(1), .lowDuration(1)) CLK (.out(CLK_out));
  D_Flip_Flop #(.trigger("rising")) d_ff_1 (
    .clk(CLK_out), .D(DATA), .Q(d_ff_1_q), .reset(RST));  // open: Qn, preset, en
  D_Flip_Flop #(.trigger("rising")) d_ff_2 (
    .clk(CLK_out), .D(d_ff_1_q), .Q(d_ff_2_q), .reset(RST));  // open: Qn, preset, en
  D_Flip_Flop #(.trigger("rising")) d_ff_3 (
    .clk(CLK_out), .D(d_ff_2_q), .Q(d_ff_3_q), .reset(RST));  // open: Qn, preset, en
  not not_1 (not_1_out, d_ff_2_q);
  and and_1 (out_3, d_ff_3_q, not_1_out, d_ff_1_q);

  // Notes on the sheet:
  //   Detecção 101
  //   Celso R França Jr.
endmodule

module exe02 (
  input  DATA,
  input  RST,
  output out_3
);

  wire and_1_out, CLK_out, d_ff_1_q, d_ff_2_q, d_ff_3_q, d_ff_4_q, not_1_out, not_2_out, or_1_out;

  Clock #(.highDuration(1), .lowDuration(1)) CLK (.out(CLK_out));
  or or_1 (or_1_out, RST, out_3);
  D_Flip_Flop #(.trigger("rising")) d_ff_1 (
    .clk(CLK_out), .D(DATA), .Q(d_ff_1_q), .reset(or_1_out));  // open: Qn, preset, en
  D_Flip_Flop #(.trigger("rising")) d_ff_2 (
    .clk(CLK_out), .D(d_ff_1_q), .Q(d_ff_2_q), .reset(or_1_out));  // open: Qn, preset, en
  D_Flip_Flop #(.trigger("rising")) d_ff_3 (
    .clk(CLK_out), .D(d_ff_4_q), .Q(d_ff_3_q), .reset(or_1_out));  // open: Qn, preset, en
  D_Flip_Flop #(.trigger("rising")) d_ff_4 (
    .clk(CLK_out), .D(d_ff_2_q), .Q(d_ff_4_q), .reset(or_1_out));  // open: Qn, preset, en
  not not_1 (not_1_out, d_ff_4_q);
  not not_2 (not_2_out, d_ff_1_q);
  and and_1 (and_1_out, d_ff_3_q, not_1_out, d_ff_2_q, not_2_out);
  D_Flip_Flop #(.trigger("rising")) d_ff_5 (.clk(CLK_out), .D(and_1_out), .Q(out_3));  // open: Qn, preset, en, reset

  // Notes on the sheet:
  //   Detecção 0101
  //   Celso R França Jr.
endmodule

module exe03 (
  input  DATA,
  input  RST,
  output out_3
);

  wire CLK_out, d_ff_1_q, d_ff_2_q, d_ff_3_q, d_ff_4_q, not_1_out, not_2_out;

  Clock #(.highDuration(1), .lowDuration(1)) CLK (.out(CLK_out));
  D_Flip_Flop #(.trigger("rising")) d_ff_1 (
    .clk(CLK_out), .D(DATA), .Q(d_ff_1_q), .reset(RST));  // open: Qn, preset, en
  D_Flip_Flop #(.trigger("rising")) d_ff_2 (
    .clk(CLK_out), .D(d_ff_1_q), .Q(d_ff_2_q), .reset(RST));  // open: Qn, preset, en
  D_Flip_Flop #(.trigger("rising")) d_ff_3 (
    .clk(CLK_out), .D(d_ff_4_q), .Q(d_ff_3_q), .reset(RST));  // open: Qn, preset, en
  D_Flip_Flop #(.trigger("rising")) d_ff_4 (
    .clk(CLK_out), .D(d_ff_2_q), .Q(d_ff_4_q), .reset(RST));  // open: Qn, preset, en
  not not_1 (not_1_out, d_ff_4_q);
  not not_2 (not_2_out, d_ff_2_q);
  and and_1 (out_3, d_ff_3_q, not_1_out, not_2_out, d_ff_1_q);

  // Notes on the sheet:
  //   Detecção 1001
  //   Celso R França Jr.
endmodule

module exe04 (
  input  DATA,
  input  RST,
  output out_3
);

  wire and_1_out, and_2_out, CLK_out, d_ff_1_q, d_ff_2_q, d_ff_3_q, not_1_out, not_2_out, not_3_out;

  Clock #(.highDuration(1), .lowDuration(1)) CLK (.out(CLK_out));
  D_Flip_Flop #(.trigger("rising")) d_ff_1 (
    .clk(CLK_out), .D(DATA), .Q(d_ff_1_q), .reset(RST));  // open: Qn, preset, en
  D_Flip_Flop #(.trigger("rising")) d_ff_2 (
    .clk(CLK_out), .D(d_ff_1_q), .Q(d_ff_2_q), .reset(RST));  // open: Qn, preset, en
  D_Flip_Flop #(.trigger("rising")) d_ff_3 (
    .clk(CLK_out), .D(d_ff_2_q), .Q(d_ff_3_q), .reset(RST));  // open: Qn, preset, en
  not not_1 (not_1_out, d_ff_2_q);
  not not_2 (not_2_out, RST);
  not not_3 (not_3_out, d_ff_1_q);
  and and_1 (and_1_out, d_ff_3_q, not_1_out, d_ff_1_q);
  and and_2 (and_2_out, not_2_out, d_ff_2_q, not_3_out);
  or or_1 (out_3, and_1_out, and_2_out);

  // Notes on the sheet:
  //   Detecção 101 OU 010
  //   Celso R França Jr.
endmodule

module exe05 (
  input  DATA,
  input  RST,
  output out_3
);

  wire and_1_out, and_2_out, CLK_out, d_ff_1_q, d_ff_2_q, d_ff_3_q, not_1_out, not_2_out, not_3_out;

  Clock #(.highDuration(1), .lowDuration(1)) CLK (.out(CLK_out));
  D_Flip_Flop #(.trigger("rising")) d_ff_1 (
    .clk(CLK_out), .D(DATA), .Q(d_ff_1_q), .reset(RST));  // open: Qn, preset, en
  D_Flip_Flop #(.trigger("rising")) d_ff_2 (
    .clk(CLK_out), .D(d_ff_1_q), .Q(d_ff_2_q), .reset(RST));  // open: Qn, preset, en
  D_Flip_Flop #(.trigger("rising")) d_ff_3 (
    .clk(CLK_out), .D(d_ff_2_q), .Q(d_ff_3_q), .reset(RST));  // open: Qn, preset, en
  not not_1 (not_1_out, RST);
  not not_2 (not_2_out, d_ff_2_q);
  not not_3 (not_3_out, d_ff_1_q);
  and and_1 (and_1_out, d_ff_3_q, d_ff_2_q, d_ff_1_q);
  and and_2 (and_2_out, not_1_out, not_2_out, not_3_out);
  or or_1 (out_3, and_1_out, and_2_out);

  // Notes on the sheet:
  //   Detecção 111 OU 000
  //   Celso R França Jr.
endmodule
