// Logisim project guia_11.circ as structural Verilog: 5 circuits, main circuit ex_01
module ex_01 (
  input  data,
  input  reset,
  output out_3
);

  wire clock_out, d_ff_1_q, d_ff_2_q, d_ff_2_qn, d_ff_3_q;

  Clock #(.highDuration(1), .lowDuration(1)) clock (.out(clock_out));
  D_Flip_Flop #(.trigger("rising")) d_ff_1 (
    .clk(clock_out), .D(data), .Q(d_ff_1_q), .reset(reset));  // open: Qn, preset, en
  D_Flip_Flop #(.trigger("rising")) d_ff_2 (
    .clk(clock_out), .D(d_ff_1_q), .Q(d_ff_2_q), .Qn(d_ff_2_qn), .reset(reset));  // open: preset, en
  D_Flip_Flop #(.trigger("rising")) d_ff_3 (
    .clk(clock_out), .D(d_ff_2_q), .Q(d_ff_3_q), .reset(reset));  // open: Qn, preset, en
  and and_1 (out_3, d_ff_3_q, d_ff_2_qn, d_ff_1_q);

  // Notes on the sheet:
  //   405807
  //   José Erimá F. Júnior
endmodule

module ex_02 (
  input  data,
  input  reset,
  output out_3
);

  wire and_1_out, clock_out, d_ff_1_q, d_ff_1_qn, d_ff_2_q, d_ff_3_q, d_ff_3_qn, d_ff_4_q;

  Clock #(.highDuration(1), .lowDuration(1)) clock (.out(clock_out));
  D_Flip_Flop #(.trigger("rising")) d_ff_1 (
    .clk(clock_out), .D(data), .Q(d_ff_1_q), .Qn(d_ff_1_qn), .reset(reset));  // open: preset, en
  D_Flip_Flop #(.trigger("rising")) d_ff_2 (
    .clk(clock_out), .D(d_ff_1_q), .Q(d_ff_2_q), .reset(reset));  // open: Qn, preset, en
  D_Flip_Flop #(.trigger("rising")) d_ff_3 (
    .clk(clock_out), .D(d_ff_2_q), .Q(d_ff_3_q), .Qn(d_ff_3_qn), .reset(reset));  // open: preset, en
  D_Flip_Flop #(.trigger("rising")) d_ff_4 (
    .clk(clock_out), .D(d_ff_3_q), .Q(d_ff_4_q));  // open: Qn, preset, en, reset
  and and_1 (and_1_out, d_ff_4_q, d_ff_3_qn, d_ff_2_q, d_ff_1_qn);
  D_Flip_Flop #(.trigger("rising")) d_ff_5 (
    .clk(clock_out), .D(and_1_out), .Q(out_3), .reset(reset));  // open: Qn, preset, en
endmodule

module ex_03 (
  input  data,
  input  reset,
  output out_3
);

  wire clock_out, d_ff_1_q, d_ff_2_q, d_ff_2_qn, d_ff_3_q, d_ff_3_qn, d_ff_4_q;

  Clock #(.highDuration(1), .lowDuration(1)) clock (.out(clock_out));
  D_Flip_Flop #(.trigger("rising")) d_ff_1 (
    .clk(clock_out), .D(data), .Q(d_ff_1_q), .reset(reset));  // open: Qn, preset, en
  D_Flip_Flop #(.trigger("rising")) d_ff_2 (
    .clk(clock_out), .D(d_ff_1_q), .Q(d_ff_2_q), .Qn(d_ff_2_qn), .reset(reset));  // open: preset, en
  D_Flip_Flop #(.trigger("rising")) d_ff_3 (
    .clk(clock_out), .D(d_ff_2_q), .Q(d_ff_3_q), .Qn(d_ff_3_qn), .reset(reset));  // open: preset, en
  D_Flip_Flop #(.trigger("rising")) d_ff_4 (
    .clk(clock_out), .D(d_ff_3_q), .Q(d_ff_4_q));  // open: Qn, preset, en, reset
  and and_1 (out_3, d_ff_4_q, d_ff_3_qn, d_ff_2_qn, d_ff_1_q);
endmodule

module ex_04 (
  input  data,
  input  reset,
  output out_3
);

  wire and_1_out, and_2_out, clock_out, d_ff_1_q, d_ff_1_qn, d_ff_2_q, d_ff_2_qn, d_ff_3_q, d_ff_3_qn;

  Clock #(.highDuration(1), .lowDuration(1)) clock (.out(clock_out));
  D_Flip_Flop #(.trigger("rising")) d_ff_1 (
    .clk(clock_out), .D(data), .Q(d_ff_1_q), .Qn(d_ff_1_qn), .reset(reset));  // open: preset, en
  D_Flip_Flop #(.trigger("rising")) d_ff_2 (
    .clk(clock_out), .D(d_ff_1_q), .Q(d_ff_2_q), .Qn(d_ff_2_qn), .reset(reset));  // open: preset, en
  D_Flip_Flop #(.trigger("rising")) d_ff_3 (
    .clk(clock_out), .D(d_ff_2_q), .Q(d_ff_3_q), .Qn(d_ff_3_qn), .reset(reset));  // open: preset, en
  and and_1 (and_1_out, d_ff_3_q, d_ff_2_qn, d_ff_1_q);
  and and_2 (and_2_out, d_ff_3_qn, d_ff_2_q, d_ff_1_qn);
  or or_1 (out_3, and_1_out, and_2_out);
endmodule

module ex_05 (
  input  data,
  input  reset,
  output out_3
);

  wire and_1_out, and_2_out, clock_out, d_ff_1_q, d_ff_1_qn, d_ff_2_q, d_ff_2_qn, d_ff_3_q, d_ff_3_qn;

  Clock #(.highDuration(1), .lowDuration(1)) clock (.out(clock_out));
  D_Flip_Flop #(.trigger("rising")) d_ff_1 (
    .clk(clock_out), .D(data), .Q(d_ff_1_q), .Qn(d_ff_1_qn), .reset(reset));  // open: preset, en
  D_Flip_Flop #(.trigger("rising")) d_ff_2 (
    .clk(clock_out), .D(d_ff_1_q), .Q(d_ff_2_q), .Qn(d_ff_2_qn), .reset(reset));  // open: preset, en
  D_Flip_Flop #(.trigger("rising")) d_ff_3 (
    .clk(clock_out), .D(d_ff_2_q), .Q(d_ff_3_q), .Qn(d_ff_3_qn), .reset(reset));  // open: preset, en
  and and_1 (and_1_out, d_ff_3_q, d_ff_2_q, d_ff_1_q);
  and and_2 (and_2_out, d_ff_3_qn, d_ff_2_qn, d_ff_1_qn);
  or or_1 (out_3, and_1_out, and_2_out);
endmodule
