// Logisim project Guia1105.circ as structural Verilog: 1 circuit, main circuit main
module main (
  input  dado,
  input  Clear,
  output S
);

  wire and_1_out, and_2_out, CLK_out, d_ff_1_q, d_ff_1_qn, d_ff_2_q, d_ff_2_qn, d_ff_3_q, d_ff_3_qn,
       not_1_out, not_2_out;

  Clock #(.highDuration(1), .lowDuration(1)) CLK (.out(CLK_out));
  not not_1 (not_1_out, d_ff_2_qn);
  and and_1 (and_1_out, d_ff_1_q, not_1_out, d_ff_3_q);
  D_Flip_Flop #(.trigger("rising")) d_ff_1 (
    .clk(CLK_out), .D(dado), .Q(d_ff_1_q), .Qn(d_ff_1_qn), .reset(Clear));  // open: preset, en
  or or_1 (S, and_1_out, and_2_out);
  D_Flip_Flop #(.trigger("rising")) d_ff_2 (
    .clk(CLK_out), .D(d_ff_1_q), .Q(d_ff_2_q), .Qn(d_ff_2_qn), .reset(Clear));  // open: preset, en
  D_Flip_Flop #(.trigger("rising")) d_ff_3 (
    .clk(CLK_out), .D(d_ff_2_q), .Q(d_ff_3_q), .Qn(d_ff_3_qn), .reset(Clear));  // open: preset, en
  not not_2 (not_2_out, d_ff_2_q);
  and and_2 (and_2_out, d_ff_1_qn, not_2_out, d_ff_3_qn);

  // Notes on the sheet:
  //   Luiz Felipe Fonseca - 405817
endmodule
