// Logisim project Guia11.circ as structural Verilog: 3 circuits, main circuit Exercicio01
module Exercicio01 (
  input  in_1,
  input  RST,
  output out_3
);

  wire CLK_out, d_ff_1_q, d_ff_2_q, d_ff_2_qn, d_ff_3_q;

  Clock #(.highDuration(1), .lowDuration(1)) CLK (.out(CLK_out));
  D_Flip_Flop #(.trigger("rising")) d_ff_1 (
    .clk(CLK_out), .D(in_1), .Q(d_ff_1_q), .reset(RST));  // open: Qn, preset, en
  D_Flip_Flop #(.trigger("rising")) d_ff_2 (
    .clk(CLK_out), .D(d_ff_1_q), .Q(d_ff_2_q), .Qn(d_ff_2_qn), .reset(RST));  // open: preset, en
  D_Flip_Flop #(.trigger("rising")) d_ff_3 (
    .clk(CLK_out), .D(d_ff_2_q), .Q(d_ff_3_q), .reset(RST));  // open: Qn, preset, en
  and and_1 (out_3, d_ff_3_q, d_ff_2_qn, d_ff_1_q);

  // Notes on the sheet:
  //   Pedro Siquera- 405830
endmodule

module Exercicio02 (
  input  in_1,
  input  RST,
  output out_3
);

  wire CLK_out, d_ff_1_q, d_ff_1_qn, d_ff_2_q, d_ff_3_q, d_ff_3_qn, d_ff_4_q;

  Clock #(.highDuration(1), .lowDuration(1)) CLK (.out(CLK_out));
  D_Flip_Flop #(.trigger("rising")) d_ff_1 (
    .clk(CLK_out), .D(in_1), .Q(d_ff_1_q), .Qn(d_ff_1_qn), .reset(RST));  // open: preset, en
  D_Flip_Flop #(.trigger("rising")) d_ff_2 (
    .clk(CLK_out), .D(d_ff_1_q), .Q(d_ff_2_q), .reset(RST));  // open: Qn, preset, en
  D_Flip_Flop #(.trigger("rising")) d_ff_3 (
    .clk(CLK_out), .D(d_ff_2_q), .Q(d_ff_3_q), .Qn(d_ff_3_qn), .reset(RST));  // open: preset, en
  and and_1 (out_3, d_ff_4_q, d_ff_3_qn, d_ff_2_q, d_ff_1_qn);
  D_Flip_Flop #(.trigger("rising")) d_ff_4 (
    .clk(CLK_out), .D(d_ff_3_q), .Q(d_ff_4_q), .reset(RST));  // open: Qn, preset, en

  // Notes on the sheet:
  //   Pedro Siquera- 405830
endmodule

module Exercicio03 (
  input  in_1,
  input  RST,
  output out_3
);

  wire CLK_out, d_ff_1_q, d_ff_2_q, d_ff_2_qn, d_ff_3_q, d_ff_3_qn, d_ff_4_q;

  Clock #(.highDuration(1), .lowDuration(1)) CLK (.out(CLK_out));
  D_Flip_Flop #(.trigger("rising")) d_ff_1 (
    .clk(CLK_out), .D(in_1), .Q(d_ff_1_q), .reset(RST));  // open: Qn, preset, en
  D_Flip_Flop #(.trigger("rising")) d_ff_2 (
    .clk(CLK_out), .D(d_ff_1_q), .Q(d_ff_2_q), .Qn(d_ff_2_qn), .reset(RST));  // open: preset, en
  D_Flip_Flop #(.trigger("rising")) d_ff_3 (
    .clk(CLK_out), .D(d_ff_2_q), .Q(d_ff_3_q), .Qn(d_ff_3_qn), .reset(RST));  // open: preset, en
  and and_1 (out_3, d_ff_4_q, d_ff_3_qn, d_ff_2_qn, d_ff_1_q);
  D_Flip_Flop #(.trigger("rising")) d_ff_4 (
    .clk(CLK_out), .D(d_ff_3_q), .Q(d_ff_4_q), .reset(RST));  // open: Qn, preset, en

  // Notes on the sheet:
  //   Pedro Siqueira 405830
endmodule
