// Logisim project Exercicio02.circ as structural Verilog: 1 circuit, main circuit main
module main (
  input  D,
  input  Clr,
  output Output
);

  wire and_1_out, Clk_out, d_ff_1_q, d_ff_1_qn, d_ff_2_q, d_ff_3_q, d_ff_3_qn, d_ff_4_q, d_ff_5_q, or_1_out;

  Clock #(.highDuration(1), .lowDuration(1)) Clk (.out(Clk_out));
  D_Flip_Flop #(.trigger("rising")) d_ff_1 (
    .clk(Clk_out), .D(D), .Q(d_ff_1_q), .Qn(d_ff_1_qn), .reset(or_1_out));  // open: preset, en
  or or_1 (or_1_out, Clr, Output);
  D_Flip_Flop #(.trigger("rising")) d_ff_2 (
    .clk(Clk_out), .D(d_ff_1_q), .Q(d_ff_2_q), .reset(or_1_out));  // open: Qn, preset, en
  D_Flip_Flop #(.trigger("rising")) d_ff_3 (
    .clk(Clk_out), .D(d_ff_2_q), .Q(d_ff_3_q), .Qn(d_ff_3_qn), .reset(or_1_out));  // open: preset, en
  D_Flip_Flop #(.trigger("rising")) d_ff_4 (
    .clk(Clk_out), .D(d_ff_3_q), .Q(d_ff_4_q), .reset(or_1_out));  // open: Qn, preset, en
  and and_1 (and_1_out, d_ff_4_q, d_ff_3_qn, d_ff_2_q, d_ff_1_qn);
  D_Flip_Flop #(.trigger("rising")) d_ff_5 (.clk(Clk_out), .D(and_1_out), .Q(d_ff_5_q));  // open: Qn, preset, en, reset
  D_Flip_Flop #(.trigger("rising")) d_ff_6 (.clk(Clk_out), .D(d_ff_5_q), .Q(Output));  // open: Qn, preset, en, reset
endmodule
