// Logisim project Exercicio03.circ as structural Verilog: 1 circuit, main circuit main
module main (
  input  D,
  output Output
);

  wire Clk_out, d_ff_1_q, d_ff_2_q, d_ff_2_qn, d_ff_3_q, d_ff_3_qn, d_ff_4_q;

  Clock #(.highDuration(1), .lowDuration(1)) Clk (.out(Clk_out));
  D_Flip_Flop #(.trigger("rising")) d_ff_1 (.clk(Clk_out), .D(D), .Q(d_ff_1_q));  // open: Qn, preset, en, reset
  D_Flip_Flop #(.trigger("rising")) d_ff_2 (
    .clk(Clk_out), .D(d_ff_1_q), .Q(d_ff_2_q), .Qn(d_ff_2_qn));  // open: preset, en, reset
  D_Flip_Flop #(.trigger("rising")) d_ff_3 (
    .clk(Clk_out), .D(d_ff_2_q), .Q(d_ff_3_q), .Qn(d_ff_3_qn));  // open: preset, en, reset
  D_Flip_Flop #(.trigger("rising")) d_ff_4 (.clk(Clk_out), .D(d_ff_3_q), .Q(d_ff_4_q));  // open: Qn, preset, en, reset
  and and_1 (Output, d_ff_4_q, d_ff_3_qn, d_ff_2_qn, d_ff_1_q);
endmodule
