// Logisim project Exercicios_guia11.circ as structural Verilog: 5 circuits, main circuit Exercicio01_guia11
module Exercicio01_guia11 (
  input  in_1,
  input  RESET,
  output SAIDA
);

  wire CLOCK_out, d_ff_1_q, d_ff_2_q, d_ff_2_qn, d_ff_3_q;

  Clock #(.highDuration(1), .lowDuration(1)) CLOCK (.out(CLOCK_out));
  D_Flip_Flop #(.trigger("rising")) d_ff_1 (
    .clk(CLOCK_out), .D(in_1), .Q(d_ff_1_q), .reset(RESET));  // open: Qn, preset, en
  D_Flip_Flop #(.trigger("rising")) d_ff_2 (
    .clk(CLOCK_out), .D(d_ff_1_q), .Q(d_ff_2_q), .Qn(d_ff_2_qn), .reset(RESET));  // open: preset, en
  D_Flip_Flop #(.trigger("rising")) d_ff_3 (
    .clk(CLOCK_out), .D(d_ff_2_q), .Q(d_ff_3_q), .reset(RESET));  // open: Qn, preset, en
  and and_1 (SAIDA, d_ff_1_q, d_ff_2_qn, d_ff_3_q);

  // Notes on the sheet:
  //   Exercicio01_guia11
  //   Marcos Felipe Martins Silva-415719
  //   Sequencia-101
  //   1_saida reconhecida
  //   0-saida nao reconhecida
endmodule

module Exercicio02 (
  input  in_1,
  input  RESET,
  output SAIDA
);

  wire and_1_out, CLOCK_out, d_ff_1_q, d_ff_1_qn, d_ff_2_q, d_ff_3_q, d_ff_3_qn, d_ff_4_q, or_1_out;

  Clock #(.highDuration(1), .lowDuration(1)) CLOCK (.out(CLOCK_out));
  or or_1 (or_1_out, RESET, SAIDA);
  D_Flip_Flop #(.trigger("rising")) d_ff_1 (
    .clk(CLOCK_out), .D(in_1), .Q(d_ff_1_q), .Qn(d_ff_1_qn), .reset(or_1_out));  // open: preset, en
  D_Flip_Flop #(.trigger("rising")) d_ff_2 (
    .clk(CLOCK_out), .D(d_ff_1_q), .Q(d_ff_2_q), .reset(or_1_out));  // open: Qn, preset, en
  D_Flip_Flop #(.trigger("rising")) d_ff_3 (
    .clk(CLOCK_out), .D(d_ff_2_q), .Q(d_ff_3_q), .Qn(d_ff_3_qn), .reset(or_1_out));  // open: preset, en
  D_Flip_Flop #(.trigger("rising")) d_ff_4 (
    .clk(CLOCK_out), .D(d_ff_3_q), .Q(d_ff_4_q), .reset(or_1_out));  // open: Qn, preset, en
  and and_1 (and_1_out, d_ff_1_qn, d_ff_2_q, d_ff_3_qn, d_ff_4_q);
  D_Flip_Flop #(.trigger("rising")) d_ff_5 (.clk(CLOCK_out), .D(and_1_out), .Q(SAIDA));  // open: Qn, preset, en, reset

  // Notes on the sheet:
  //   Exercicio02_guia11
  //   Marcos Felipe Martins Silva-415719
  //   Sequencia-0101
  //   1_saida reconhecida
  //   0-saida nao reconhecida
endmodule

module Exercicio03 (
  input  in_1,
  input  RESET,
  output SAIDA
);

  wire CLOCK_out, d_ff_1_q, d_ff_2_q, d_ff_2_qn, d_ff_3_q, d_ff_3_qn, d_ff_4_q;

  Clock #(.highDuration(1), .lowDuration(1)) CLOCK (.out(CLOCK_out));
  D_Flip_Flop #(.trigger("rising")) d_ff_1 (
    .clk(CLOCK_out), .D(in_1), .Q(d_ff_1_q), .reset(RESET));  // open: Qn, preset, en
  D_Flip_Flop #(.trigger("rising")) d_ff_2 (
    .clk(CLOCK_out), .D(d_ff_1_q), .Q(d_ff_2_q), .Qn(d_ff_2_qn), .reset(RESET));  // open: preset, en
  D_Flip_Flop #(.trigger("rising")) d_ff_3 (
    .clk(CLOCK_out), .D(d_ff_2_q), .Q(d_ff_3_q), .Qn(d_ff_3_qn), .reset(RESET));  // open: preset, en
  D_Flip_Flop #(.trigger("rising")) d_ff_4 (
    .clk(CLOCK_out), .D(d_ff_3_q), .Q(d_ff_4_q), .reset(RESET));  // open: Qn, preset, en
  and and_1 (SAIDA, d_ff_1_q, d_ff_2_qn, d_ff_3_qn, d_ff_4_q);

  // Notes on the sheet:
  //   Exercicio03_guia11
  //   Marcos Felipe Martins Silva-415719
  //   Sequencia-1001
  //   1_saida reconhecida
  //   0-saida nao reconhecida
endmodule

module Exercicio04 (
  input  in_1,
  input  RESET,
  output SAIDA
);

  wire and_1_out, and_2_out, CLOCK_out, d_ff_1_q, d_ff_1_qn, d_ff_2_q, d_ff_2_qn, d_ff_3_q, d_ff_3_qn;

  Clock #(.highDuration(1), .lowDuration(1)) CLOCK (.out(CLOCK_out));
  D_Flip_Flop #(.trigger("rising")) d_ff_1 (
    .clk(CLOCK_out), .D(in_1), .Q(d_ff_1_q), .Qn(d_ff_1_qn), .reset(RESET));  // open: preset, en
  D_Flip_Flop #(.trigger("rising")) d_ff_2 (
    .clk(CLOCK_out), .D(d_ff_1_q), .Q(d_ff_2_q), .Qn(d_ff_2_qn), .reset(RESET));  // open: preset, en
  D_Flip_Flop #(.trigger("rising")) d_ff_3 (
    .clk(CLOCK_out), .D(d_ff_2_q), .Q(d_ff_3_q), .Qn(d_ff_3_qn), .reset(RESET));  // open: preset, en
  and and_1 (and_1_out, d_ff_1_q, d_ff_2_qn, d_ff_3_q);
  and and_2 (and_2_out, d_ff_1_qn, d_ff_2_q, d_ff_3_qn);
  or or_1 (SAIDA, and_1_out, and_2_out);

  // Notes on the sheet:
  //   Exercicio04_guia11
  //   Marcos Felipe Martins Silva-415719
  //   Sequencia-010 OU 101
  //   1_saida reconhecida
  //   0-saida nao reconhecida
endmodule

module Exercicio05 (
  input  in_1,
  input  RESET,
  output SAIDA
);

  wire and_1_out, and_2_out, CLOCK_out, d_ff_1_q, d_ff_1_qn, d_ff_2_q, d_ff_2_qn, d_ff_3_q, d_ff_3_qn;

  Clock #(.highDuration(1), .lowDuration(1)) CLOCK (.out(CLOCK_out));
  D_Flip_Flop #(.trigger("rising")) d_ff_1 (
    .clk(CLOCK_out), .D(in_1), .Q(d_ff_1_q), .Qn(d_ff_1_qn), .reset(RESET));  // open: preset, en
  D_Flip_Flop #(.trigger("rising")) d_ff_2 (
    .clk(CLOCK_out), .D(d_ff_1_q), .Q(d_ff_2_q), .Qn(d_ff_2_qn), .reset(RESET));  // open: preset, en
  D_Flip_Flop #(.trigger("rising")) d_ff_3 (
    .clk(CLOCK_out), .D(d_ff_2_q), .Q(d_ff_3_q), .Qn(d_ff_3_qn), .reset(RESET));  // open: preset, en
  and and_1 (and_1_out, d_ff_3_q, d_ff_2_q, d_ff_1_q);
  and and_2 (and_2_out, d_ff_1_qn, d_ff_2_qn, d_ff_3_qn);
  or or_1 (SAIDA, and_1_out, and_2_out);

  // Notes on the sheet:
  //   Exercicio05_guia11
  //   Marcos Felipe Martins Silva-415719
  //   Sequencia-000 OU 111
  //   1_saida reconhecida
  //   0-saida nao reconhecida
endmodule
