// Logisim project circuito maquinadeestadofinito.circ as structural Verilog: 1 circuit, main circuit circuito maquinadeestadosfinitos.circmain
module circuito_maquinadeestadosfinitos_circmain (
  input  in_1,
  input  in_2
);

  wire clock_1_out, s_r_ff_1_q, s_r_ff_1_qn, s_r_ff_2_qn, s_r_ff_3_q;

  Clock #(.highDuration(1), .lowDuration(1)) clock_1 (.out(clock_1_out));
  S_R_Flip_Flop #(.trigger("rising")) s_r_ff_1 (
    .S(s_r_ff_1_q), .clk(clock_1_out), .R(in_1), .Q(s_r_ff_1_q), .Qn(s_r_ff_1_qn), .reset(in_2));  // open: preset, en
  S_R_Flip_Flop #(.trigger("rising")) s_r_ff_2 (
    .clk(clock_1_out), .Qn(s_r_ff_2_qn), .reset(in_2));  // open: S, R, Q, preset, en
  S_R_Flip_Flop #(.trigger("rising")) s_r_ff_3 (
    .clk(clock_1_out), .Q(s_r_ff_3_q), .reset(in_2));  // open: S, R, Qn, preset, en
  Priority_Encoder #(.select(3)) priority_encoder_1 (
    .in0(s_r_ff_3_q), .in4(s_r_ff_2_qn), .in7(s_r_ff_1_qn));  // open: in1, in2, in3, in5, in6, out, en_in, gs, en_out

  // Notes on the sheet:
  //   Nome:Eneas ,Numero:376507
  //   O CLR deve ser ligado assim
  //   circuito maquina de estados finitos
  //   nao ha' sinal chegando nas entradas de controle
  //   nao ha' necessidade disso
endmodule
