// Logisim project Circuitos.circ as structural Verilog: 5 circuits, main circuit Sequencia 101 com intersecao
module Sequencia_101_com_intersecao (
  input  _1,
  input  Reset,
  output S1
);

  wire Clock_out, d_ff_1_q, d_ff_2_q, d_ff_2_qn, d_ff_3_q;

  Clock #(.highDuration(1), .lowDuration(1)) Clock (.out(Clock_out));
  D_Flip_Flop #(.trigger("rising")) d_ff_1 (
    .clk(Clock_out), .D(_1), .Q(d_ff_1_q), .reset(Reset));  // open: Qn, preset, en
  D_Flip_Flop #(.trigger("rising")) d_ff_2 (
    .clk(Clock_out), .D(d_ff_1_q), .Q(d_ff_2_q), .Qn(d_ff_2_qn), .reset(Reset));  // open: preset, en
  D_Flip_Flop #(.trigger("rising")) d_ff_3 (
    .clk(Clock_out), .D(d_ff_2_q), .Q(d_ff_3_q), .reset(Reset));  // open: Qn, preset, en
  and and_1 (S1, d_ff_1_q, d_ff_2_qn, d_ff_3_q);

  // Notes on the sheet:
  //   Nádia de Souza Maciel Vieira Ferreira
  //   guia 11
endmodule

module Sequencia_0101_sem_intersecao (
  input  _1,
  input  Reset,
  output out_3
);

  wire and_1_out, Clock_out, d_ff_1_q, d_ff_1_qn, d_ff_2_q, d_ff_3_q, d_ff_3_qn, d_ff_4_q, or_1_out;

  Clock #(.highDuration(1), .lowDuration(1)) Clock (.out(Clock_out));
  or or_1 (or_1_out, Reset, out_3);
  D_Flip_Flop #(.trigger("rising")) d_ff_1 (
    .clk(Clock_out), .D(_1), .Q(d_ff_1_q), .Qn(d_ff_1_qn), .reset(or_1_out));  // open: preset, en
  D_Flip_Flop #(.trigger("rising")) d_ff_2 (
    .clk(Clock_out), .D(d_ff_1_q), .Q(d_ff_2_q), .reset(or_1_out));  // open: Qn, preset, en
  D_Flip_Flop #(.trigger("rising")) d_ff_3 (
    .clk(Clock_out), .D(d_ff_2_q), .Q(d_ff_3_q), .Qn(d_ff_3_qn), .reset(or_1_out));  // open: preset, en
  D_Flip_Flop #(.trigger("rising")) d_ff_4 (
    .clk(Clock_out), .D(d_ff_3_q), .Q(d_ff_4_q), .reset(or_1_out));  // open: Qn, preset, en
  and and_1 (and_1_out, d_ff_1_qn, d_ff_2_q, d_ff_3_qn, d_ff_4_q);
  D_Flip_Flop #(.trigger("rising")) d_ff_5 (.clk(Clock_out), .D(and_1_out), .Q(out_3));  // open: Qn, preset, en, reset

  // Notes on the sheet:
  //   guia 11
  //   Nádia de Souza Maciel Vieira Ferreira 
endmodule

module Sequencia_1001_com_intersecao (
  input  in_1,
  input  in_2,
  output out_3
);

  wire clock_1_out, d_ff_1_q, d_ff_2_q, d_ff_2_qn, d_ff_3_q, d_ff_3_qn, d_ff_4_q;

  Clock #(.highDuration(1), .lowDuration(1)) clock_1 (.out(clock_1_out));
  D_Flip_Flop #(.trigger("rising")) d_ff_1 (
    .clk(clock_1_out), .D(in_1), .Q(d_ff_1_q), .reset(in_2));  // open: Qn, preset, en
  D_Flip_Flop #(.trigger("rising")) d_ff_2 (
    .clk(clock_1_out), .D(d_ff_1_q), .Q(d_ff_2_q), .Qn(d_ff_2_qn), .reset(in_2));  // open: preset, en
  D_Flip_Flop #(.trigger("rising")) d_ff_3 (
    .clk(clock_1_out), .D(d_ff_2_q), .Q(d_ff_3_q), .Qn(d_ff_3_qn), .reset(in_2));  // open: preset, en
  D_Flip_Flop #(.trigger("rising")) d_ff_4 (
    .clk(clock_1_out), .D(d_ff_3_q), .Q(d_ff_4_q), .reset(in_2));  // open: Qn, preset, en
  and and_1 (out_3, d_ff_1_q, d_ff_2_qn, d_ff_3_qn, d_ff_4_q);

  // Notes on the sheet:
  //   Nádia de souza Maciel Vieira Ferreira 
  //   guia11
endmodule

module Sequencia_101_ou_010 (
  input  _1,
  input  Reset,
  output S1
);

  wire and_1_out, and_2_out, Clock_out, d_ff_1_q, d_ff_1_qn, d_ff_2_q, d_ff_2_qn, d_ff_3_q, d_ff_3_qn;

  Clock #(.highDuration(1), .lowDuration(1)) Clock (.out(Clock_out));
  D_Flip_Flop #(.trigger("rising")) d_ff_1 (
    .clk(Clock_out), .D(_1), .Q(d_ff_1_q), .Qn(d_ff_1_qn), .reset(Reset));  // open: preset, en
  D_Flip_Flop #(.trigger("rising")) d_ff_2 (
    .clk(Clock_out), .D(d_ff_1_q), .Q(d_ff_2_q), .Qn(d_ff_2_qn), .reset(Reset));  // open: preset, en
  D_Flip_Flop #(.trigger("rising")) d_ff_3 (
    .clk(Clock_out), .D(d_ff_2_q), .Q(d_ff_3_q), .Qn(d_ff_3_qn), .reset(Reset));  // open: preset, en
  and and_1 (and_1_out, d_ff_1_q, d_ff_2_qn, d_ff_3_q);
  and and_2 (and_2_out, d_ff_1_qn, d_ff_2_q, d_ff_3_qn);
  or or_1 (S1, and_1_out, and_2_out);

  // Notes on the sheet:
  //   Nadia de souza maciel vieira ferreira
endmodule

module Sequencia_000_ou_111 (
  input  _1,
  input  Reset,
  output out_3
);

  wire and_1_out, and_2_out, Clock_out, d_ff_1_q, d_ff_1_qn, d_ff_2_q, d_ff_2_qn, d_ff_3_q, d_ff_3_qn;

  Clock #(.highDuration(1), .lowDuration(1)) Clock (.out(Clock_out));
  D_Flip_Flop #(.trigger("rising")) d_ff_1 (
    .clk(Clock_out), .D(_1), .Q(d_ff_1_q), .Qn(d_ff_1_qn), .reset(Reset));  // open: preset, en
  D_Flip_Flop #(.trigger("rising")) d_ff_2 (
    .clk(Clock_out), .D(d_ff_1_q), .Q(d_ff_2_q), .Qn(d_ff_2_qn), .reset(Reset));  // open: preset, en
  D_Flip_Flop #(.trigger("rising")) d_ff_3 (
    .clk(Clock_out), .D(d_ff_2_q), .Q(d_ff_3_q), .Qn(d_ff_3_qn), .reset(Reset));  // open: preset, en
  and and_1 (and_1_out, d_ff_3_q, d_ff_2_q, d_ff_1_q);
  and and_2 (and_2_out, d_ff_1_qn, d_ff_2_qn, d_ff_3_qn);
  or or_1 (out_3, and_1_out, and_2_out);

  // Notes on the sheet:
  //   nadia de souza maciel vieira ferreira
endmodule
