// Logisim project Exe01.circ as structural Verilog: 1 circuit, main circuit main
module main (
  input  clear,
  input  dado,
  output S
);

  wire CLK_out, d_ff_1_q, d_ff_2_q, d_ff_3_q, not_1_out, not_2_out;

  Clock #(.highDuration(1), .lowDuration(1)) CLK (.out(CLK_out));
  D_Flip_Flop #(.trigger("rising")) d_ff_1 (
    .clk(CLK_out), .D(dado), .Q(d_ff_1_q), .reset(clear));  // open: Qn, preset, en
  D_Flip_Flop #(.trigger("rising")) d_ff_2 (
    .clk(CLK_out), .D(not_1_out), .Q(d_ff_2_q), .reset(clear));  // open: Qn, preset, en
  not not_1 (not_1_out, d_ff_1_q);
  D_Flip_Flop #(.trigger("rising")) d_ff_3 (
    .clk(CLK_out), .D(d_ff_2_q), .Q(d_ff_3_q), .reset(clear));  // open: Qn, preset, en
  not not_2 (not_2_out, d_ff_2_q);
  and and_1 (S, d_ff_3_q, not_2_out, d_ff_1_q);

  // Notes on the sheet:
  //   Bruno César Lopes Silva - 415985
endmodule
