// Logisim project Exe02.circ as structural Verilog: 1 circuit, main circuit main
module main (
  input  dado,
  input  clear,
  output S
);

  wire and_1_out, CLK_out, d_ff_1_q, d_ff_2_q, d_ff_3_q, d_ff_4_q, not_1_out;

  Clock #(.highDuration(1), .lowDuration(1)) CLK (.out(CLK_out));
  D_Flip_Flop #(.trigger("rising")) d_ff_1 (
    .clk(CLK_out), .D(dado), .Q(d_ff_1_q), .reset(clear));  // open: Qn, preset, en
  not not_1 (not_1_out, d_ff_1_q);
  D_Flip_Flop #(.trigger("rising")) d_ff_2 (
    .clk(CLK_out), .D(not_1_out), .Q(d_ff_2_q), .reset(clear));  // open: Qn, preset, en
  and and_1 (and_1_out, d_ff_4_q, d_ff_3_q, d_ff_2_q, d_ff_1_q);
  D_Flip_Flop #(.trigger("rising")) d_ff_3 (
    .clk(CLK_out), .D(d_ff_2_q), .Q(d_ff_3_q), .reset(clear));  // open: Qn, preset, en
  D_Flip_Flop #(.trigger("rising")) d_ff_4 (
    .clk(CLK_out), .D(CLK_out), .Q(d_ff_4_q), .reset(clear));  // open: Qn, preset, en
  D_Flip_Flop #(.trigger("rising")) d_ff_5 (
    .clk(CLK_out), .D(and_1_out), .Q(S), .en(clear));  // open: Qn, preset, reset

  // Notes on the sheet:
  //   Bruno César Lopes Silva - 415985
endmodule
