// Logisim project Guia12.circ as structural Verilog: 5 circuits, main circuit main
module main (
  input  dado__in,
  input  clear,
  output dado__out
);

  wire clk_out, j_k_ff_1_q, j_k_ff_1_qn, j_k_ff_2_q, j_k_ff_2_qn, j_k_ff_3_q, j_k_ff_3_qn, j_k_ff_4_q,
       j_k_ff_4_qn, not_1_out;

  Clock #(.highDuration(1), .lowDuration(1)) clk (.out(clk_out));
  not not_1 (not_1_out, dado__in);
  J_K_Flip_Flop #(.trigger("rising")) j_k_ff_1 (
    .J(dado__in), .clk(clk_out), .K(not_1_out), .Q(j_k_ff_1_q), .Qn(j_k_ff_1_qn), .reset(clear));  // open: preset, en
  J_K_Flip_Flop #(.trigger("rising")) j_k_ff_2 (
    .J(j_k_ff_1_q), .clk(clk_out), .K(j_k_ff_1_qn), .Q(j_k_ff_2_q), .Qn(j_k_ff_2_qn), .reset(clear));  // open: preset, en
  J_K_Flip_Flop #(.trigger("rising")) j_k_ff_3 (
    .J(j_k_ff_2_q), .clk(clk_out), .K(j_k_ff_2_qn), .Q(j_k_ff_3_q), .Qn(j_k_ff_3_qn), .reset(clear));  // open: preset, en
  J_K_Flip_Flop #(.trigger("rising")) j_k_ff_4 (
    .J(j_k_ff_3_q), .clk(clk_out), .K(j_k_ff_3_qn), .Q(j_k_ff_4_q), .Qn(j_k_ff_4_qn), .reset(clear));  // open: preset, en
  J_K_Flip_Flop #(.trigger("rising")) j_k_ff_5 (
    .J(j_k_ff_4_q), .clk(clk_out), .K(j_k_ff_4_qn), .Q(dado__out), .reset(clear));  // open: Qn, preset, en

  // Notes on the sheet:
  //   Testes
  //   A cada variação do clock o valor em dado (in)
  //   se propaga ao longo das celulas (para a direita).
  //   Registrador de Deslocameto (Direita)
  //   Celso R França Jr
endmodule

module exe02 (
  input  in_1,
  input  clear,
  input  load,
  input  a,
  input  b,
  input  c,
  input  d,
  input  e,
  input  in_9,
  input  clear_2,
  input  load_2,
  input  a_2,
  input  b_2,
  input  c_2,
  input  d_2,
  input  e_2,
  output out_17,
  output out_18
);

  wire and_1_out, and_2_out, and_3_out, and_4_out, and_5_out, and_6_out, and_7_out, and_8_out, and_9_out,
       and_10_out, CLK_2_out, CLK_out, j_k_ff_1_q, j_k_ff_1_qn, j_k_ff_2_q, j_k_ff_2_qn, j_k_ff_3_q,
       j_k_ff_3_qn, j_k_ff_4_q, j_k_ff_4_qn, not_1_out, not_2_out, s_r_ff_1_q, s_r_ff_1_qn, s_r_ff_2_q,
       s_r_ff_2_qn, s_r_ff_3_q, s_r_ff_3_qn, s_r_ff_4_q, s_r_ff_4_qn;

  Clock #(.highDuration(1), .lowDuration(1)) CLK (.out(CLK_out));
  not not_1 (not_1_out, in_1);
  Clock #(.highDuration(1), .lowDuration(1)) CLK_2 (.out(CLK_2_out));
  not not_2 (not_2_out, in_9);
  J_K_Flip_Flop #(.trigger("rising")) j_k_ff_1 (
    .J(in_1), .clk(CLK_out), .K(not_1_out), .Q(j_k_ff_1_q), .Qn(j_k_ff_1_qn), .preset(and_1_out),
    .reset(clear));  // open: en
  and and_1 (and_1_out, a, load);
  S_R_Flip_Flop #(.trigger("rising")) s_r_ff_1 (
    .S(in_9), .clk(CLK_2_out), .R(not_2_out), .Q(s_r_ff_1_q), .Qn(s_r_ff_1_qn), .preset(and_2_out),
    .reset(clear_2));  // open: en
  and and_2 (and_2_out, a_2, load_2);
  J_K_Flip_Flop #(.trigger("rising")) j_k_ff_2 (
    .J(j_k_ff_1_q), .clk(CLK_out), .K(j_k_ff_1_qn), .Q(j_k_ff_2_q), .Qn(j_k_ff_2_qn), .preset(and_3_out),
    .reset(clear));  // open: en
  and and_3 (and_3_out, b, load);
  S_R_Flip_Flop #(.trigger("rising")) s_r_ff_2 (
    .S(s_r_ff_1_q), .clk(CLK_2_out), .R(s_r_ff_1_qn), .Q(s_r_ff_2_q), .Qn(s_r_ff_2_qn), .preset(and_4_out),
    .reset(clear_2));  // open: en
  and and_4 (and_4_out, b_2, load_2);
  J_K_Flip_Flop #(.trigger("rising")) j_k_ff_3 (
    .J(j_k_ff_2_q), .clk(CLK_out), .K(j_k_ff_2_qn), .Q(j_k_ff_3_q), .Qn(j_k_ff_3_qn), .preset(and_5_out),
    .reset(clear));  // open: en
  and and_5 (and_5_out, c, load);
  and and_6 (and_6_out, d, load);
  S_R_Flip_Flop #(.trigger("rising")) s_r_ff_3 (
    .S(s_r_ff_2_q), .clk(CLK_2_out), .R(s_r_ff_2_qn), .Q(s_r_ff_3_q), .Qn(s_r_ff_3_qn), .preset(and_8_out),
    .reset(clear_2));  // open: en
  and and_7 (and_7_out, d_2, load_2);
  and and_8 (and_8_out, c_2, load_2);
  J_K_Flip_Flop #(.trigger("rising")) j_k_ff_4 (
    .J(j_k_ff_3_q), .clk(CLK_out), .K(j_k_ff_3_qn), .Q(j_k_ff_4_q), .Qn(j_k_ff_4_qn), .preset(and_6_out),
    .reset(clear));  // open: en
  and and_9 (and_9_out, e, load);
  S_R_Flip_Flop #(.trigger("rising")) s_r_ff_4 (
    .S(s_r_ff_3_q), .clk(CLK_2_out), .R(s_r_ff_3_qn), .Q(s_r_ff_4_q), .Qn(s_r_ff_4_qn), .preset(and_7_out),
    .reset(clear_2));  // open: en
  and and_10 (and_10_out, e_2, load_2);
  J_K_Flip_Flop #(.trigger("rising")) j_k_ff_5 (
    .J(j_k_ff_4_q), .clk(CLK_out), .K(j_k_ff_4_qn), .Q(out_17), .preset(and_9_out), .reset(clear));  // open: Qn, en
  S_R_Flip_Flop #(.trigger("rising")) s_r_ff_5 (
    .S(s_r_ff_4_q), .clk(CLK_2_out), .R(s_r_ff_4_qn), .Q(out_18), .preset(and_10_out), .reset(clear_2));  // open: Qn, en

  // Notes on the sheet:
  //   Conversor Serie-Paralelo
  //   Testes
  //   esse dados sao propagados em as celulas
  //   Celso R França Jr
  //   Ao carregar os os bits (a-b) e load em 1
  //   vizinhas de forma serial
endmodule

module exe03 (
  input  reset
);

  wire clock_1_out, j_k_ff_2_q, j_k_ff_3_q, not_1_out, not_2_out, not_3_out, not_4_out, not_5_out, not_6_out;

  Clock #(.highDuration(1), .lowDuration(1)) clock_1 (.out(clock_1_out));
  not not_1 (not_1_out, j_k_ff_2_q);
  J_K_Flip_Flop #(.trigger("rising")) j_k_ff_1 (
    .J(1'b1), .clk(not_1_out), .K(1'b1), .preset(not_2_out), .reset(reset));  // open: Q, Qn, en
  not not_2 (not_2_out, 1'b1);
  not not_3 (not_3_out, j_k_ff_3_q);
  not not_4 (not_4_out, 1'b1);
  J_K_Flip_Flop #(.trigger("rising")) j_k_ff_2 (
    .J(1'b1), .clk(not_3_out), .K(1'b1), .Q(j_k_ff_2_q), .preset(not_4_out), .reset(reset));  // open: Qn, en
  not not_5 (not_5_out, clock_1_out);
  not not_6 (not_6_out, 1'b1);
  J_K_Flip_Flop #(.trigger("rising")) j_k_ff_3 (
    .J(1'b1), .clk(not_5_out), .K(1'b1), .Q(j_k_ff_3_q), .preset(not_6_out), .reset(reset));  // open: Qn, en

  // Notes on the sheet:
  //   Testes
  //   A cada pulso do clock e realizado uma
  //   contagem binaria de ate 3bits ( crescente)
  //    Contador de Pulso (crescente)
  //   Celso R França Jr
endmodule

module exe04 (
  input  dados__in
);

  wire clock_1_out, j_k_ff_2_q, j_k_ff_2_qn, j_k_ff_3_q, j_k_ff_3_qn, j_k_ff_4_q, j_k_ff_4_qn, j_k_ff_5_q,
       j_k_ff_5_qn, not_1_out;

  Clock #(.highDuration(1), .lowDuration(1)) clock_1 (.out(clock_1_out));
  J_K_Flip_Flop #(.trigger("rising")) j_k_ff_1 (
    .J(j_k_ff_2_q), .clk(clock_1_out), .K(j_k_ff_2_qn));  // open: Q, Qn, preset, en, reset
  J_K_Flip_Flop #(.trigger("rising")) j_k_ff_2 (
    .J(j_k_ff_3_q), .clk(clock_1_out), .K(j_k_ff_3_qn), .Q(j_k_ff_2_q), .Qn(j_k_ff_2_qn));  // open: preset, en, reset
  J_K_Flip_Flop #(.trigger("rising")) j_k_ff_3 (
    .J(j_k_ff_4_q), .clk(clock_1_out), .K(j_k_ff_4_qn), .Q(j_k_ff_3_q), .Qn(j_k_ff_3_qn));  // open: preset, en, reset
  J_K_Flip_Flop #(.trigger("rising")) j_k_ff_4 (
    .J(j_k_ff_5_q), .clk(clock_1_out), .K(j_k_ff_5_qn), .Q(j_k_ff_4_q), .Qn(j_k_ff_4_qn));  // open: preset, en, reset
  J_K_Flip_Flop #(.trigger("rising")) j_k_ff_5 (
    .J(dados__in), .clk(clock_1_out), .K(not_1_out), .Q(j_k_ff_5_q), .Qn(j_k_ff_5_qn));  // open: preset, en, reset
  not not_1 (not_1_out, dados__in);

  // Notes on the sheet:
  //   Testes
  //   A cada variação do clock o valor em dado (in)
  //   se propaga ao longo das celulas.(para a esquerda)
  //   Registrador de Deslocameto ( Esqueda )
  //   Celso R França Jr
endmodule

module exe05 (
  input  reset
);

  wire clock_1_out, j_k_ff_2_q, j_k_ff_3_q, not_1_out, not_2_out, not_3_out;

  Clock #(.highDuration(1), .lowDuration(1)) clock_1 (.out(clock_1_out));
  J_K_Flip_Flop #(.trigger("rising")) j_k_ff_1 (
    .J(1'b1), .clk(j_k_ff_2_q), .K(1'b1), .preset(not_1_out), .reset(reset));  // open: Q, Qn, en
  not not_1 (not_1_out, 1'b1);
  not not_2 (not_2_out, 1'b1);
  J_K_Flip_Flop #(.trigger("rising")) j_k_ff_2 (
    .J(1'b1), .clk(j_k_ff_3_q), .K(1'b1), .Q(j_k_ff_2_q), .preset(not_2_out), .reset(reset));  // open: Qn, en
  not not_3 (not_3_out, 1'b1);
  J_K_Flip_Flop #(.trigger("rising")) j_k_ff_3 (
    .J(1'b1), .clk(clock_1_out), .K(1'b1), .Q(j_k_ff_3_q), .preset(not_3_out), .reset(reset));  // open: Qn, en

  // Notes on the sheet:
  //   Testes
  //   A cada pulso do clock e realizado uma
  //   contagem binaria de ate 3bits (decresente)
  //    Contador de Pulso (decrescente)
  //   Celso R França Jr
endmodule
