// Logisim project circuitos_sequenciais.circ as structural Verilog: 5 circuits, main circuit registrador_dir_5bits
module registrador_dir_5bits (
  input  \input ,
  input  Clear,
  output a,
  output b,
  output c,
  output d,
  output e
);

  wire clock_out, or_1_out;

  Clock #(.highDuration(1), .lowDuration(1)) clock (.out(clock_out));
  D_Flip_Flop #(.trigger("rising")) d_ff_1 (
    .clk(clock_out), .D(or_1_out), .Q(a), .reset(Clear));  // open: Qn, preset, en
  or or_1 (or_1_out, e, \input );
  D_Flip_Flop #(.trigger("rising")) d_ff_2 (.clk(clock_out), .D(a), .Q(b), .reset(Clear));  // open: Qn, preset, en
  D_Flip_Flop #(.trigger("rising")) d_ff_3 (.clk(clock_out), .D(b), .Q(c), .reset(Clear));  // open: Qn, preset, en
  D_Flip_Flop #(.trigger("rising")) d_ff_4 (.clk(clock_out), .D(c), .Q(d), .reset(Clear));  // open: Qn, preset, en
  D_Flip_Flop #(.trigger("rising")) d_ff_5 (.clk(clock_out), .D(d), .Q(e), .reset(Clear));  // open: Qn, preset, en

  // Notes on the sheet:
  //   Márcia Cibele Martins Carneiro - 404591
  //   Márcia Cibele Martins Carneiro - 404591
  //   Registrador de deslocamento para direita com 5 bits
endmodule

module \conversor__paralelo_série_5bits  (
  input  clear,
  input  LD,
  input  d4,
  input  d3,
  input  d2,
  input  d1,
  input  d0,
  output a,
  output b,
  output c,
  output d,
  output e
);

  wire and_1_out, and_2_out, and_3_out, and_4_out, and_5_out, clock_out;

  Clock #(.highDuration(1), .lowDuration(1)) clock (.out(clock_out));
  D_Flip_Flop #(.trigger("rising")) d_ff_1 (
    .clk(clock_out), .D(1'b0), .Q(a), .preset(and_1_out), .reset(clear));  // open: Qn, en
  and and_1 (and_1_out, LD, d4);
  D_Flip_Flop #(.trigger("rising")) d_ff_2 (
    .clk(clock_out), .D(a), .Q(b), .preset(and_2_out), .reset(clear));  // open: Qn, en
  and and_2 (and_2_out, LD, d3);
  D_Flip_Flop #(.trigger("rising")) d_ff_3 (
    .clk(clock_out), .D(b), .Q(c), .preset(and_3_out), .reset(clear));  // open: Qn, en
  and and_3 (and_3_out, LD, d2);
  D_Flip_Flop #(.trigger("rising")) d_ff_4 (
    .clk(clock_out), .D(c), .Q(d), .preset(and_4_out), .reset(clear));  // open: Qn, en
  and and_4 (and_4_out, LD, d1);
  D_Flip_Flop #(.trigger("rising")) d_ff_5 (
    .clk(clock_out), .D(d), .Q(e), .preset(and_5_out), .reset(clear));  // open: Qn, en
  and and_5 (and_5_out, LD, d0);

  // Notes on the sheet:
  //   Márcia Cibele Martins Carneiro - 404591
  //   Márcia Cibele Martins Carneiro - 404591
  //   Conversor paralelo-série com 05 bits
endmodule

module contador__pulsos__cresc_3bits (
  input  Pulso,
  input  _1,
  input  Clear,
  output a,
  output b,
  output c
);

  wire j_k_ff_2_q, j_k_ff_3_q;

  J_K_Flip_Flop #(.trigger("rising")) j_k_ff_1 (
    .J(_1), .clk(j_k_ff_2_q), .K(_1), .Qn(a), .reset(Clear));  // open: Q, preset, en
  J_K_Flip_Flop #(.trigger("rising")) j_k_ff_2 (
    .J(_1), .clk(j_k_ff_3_q), .K(_1), .Q(j_k_ff_2_q), .Qn(b), .reset(Clear));  // open: preset, en
  J_K_Flip_Flop #(.trigger("rising")) j_k_ff_3 (
    .J(_1), .clk(Pulso), .K(_1), .Q(j_k_ff_3_q), .Qn(c), .reset(Clear));  // open: preset, en

  // Notes on the sheet:
  //   Márcia Cibele Martins Carneiro - 404591
  //   Márcia Cibele Martins Carneiro - 404591
  //   Contador de pulsos crescente com 03 bits
endmodule

module registrador_esq_5bits (
  input  \input ,
  input  Clear,
  output a,
  output b,
  output c,
  output d,
  output e
);

  wire clock_out, or_1_out;

  Clock #(.highDuration(1), .lowDuration(1)) clock (.out(clock_out));
  D_Flip_Flop #(.trigger("rising")) d_ff_1 (.clk(clock_out), .D(b), .Q(a), .reset(Clear));  // open: Qn, preset, en
  or or_1 (or_1_out, a, \input );
  D_Flip_Flop #(.trigger("rising")) d_ff_2 (.clk(clock_out), .D(c), .Q(b), .reset(Clear));  // open: Qn, preset, en
  D_Flip_Flop #(.trigger("rising")) d_ff_3 (.clk(clock_out), .D(d), .Q(c), .reset(Clear));  // open: Qn, preset, en
  D_Flip_Flop #(.trigger("rising")) d_ff_4 (.clk(clock_out), .D(e), .Q(d), .reset(Clear));  // open: Qn, preset, en
  D_Flip_Flop #(.trigger("rising")) d_ff_5 (
    .clk(clock_out), .D(or_1_out), .Q(e), .reset(Clear));  // open: Qn, preset, en

  // Notes on the sheet:
  //   Márcia Cibele Martins Carneiro - 404591
  //   Márcia Cibele Martins Carneiro - 404591
  //   Registrador de deslocamento para esquerda com 5 bits
endmodule

module contador_pulsos_decres_3bits (
  input  Pulso,
  input  _1,
  input  Clear,
  output a,
  output b,
  output c
);

  J_K_Flip_Flop #(.trigger("rising")) j_k_ff_1 (.J(_1), .clk(b), .K(_1), .Qn(a), .reset(Clear));  // open: Q, preset, en
  J_K_Flip_Flop #(.trigger("rising")) j_k_ff_2 (.J(_1), .clk(c), .K(_1), .Qn(b), .reset(Clear));  // open: Q, preset, en
  J_K_Flip_Flop #(.trigger("rising")) j_k_ff_3 (
    .J(_1), .clk(Pulso), .K(_1), .Qn(c), .reset(Clear));  // open: Q, preset, en

  // Notes on the sheet:
  //   Márcia Cibele Martins Carneiro - 404591
  //   Márcia Cibele Martins Carneiro - 404591
  //   Contador de pulsos decrescente com 03 bits
endmodule
