// Logisim project G12E2.circ as structural Verilog: 1 circuit, main circuit main
module main (
  input  CLR,
  input  Load,
  input  in_3,
  input  in_4,
  input  in_5,
  input  in_6,
  input  in_7,
  output out_8
);

  wire and_1_out, and_2_out, and_3_out, and_4_out, and_5_out, CLK_out, d_ff_1_q, d_ff_2_q, d_ff_3_q, d_ff_5_q;

  Clock #(.highDuration(1), .lowDuration(1)) CLK (.out(CLK_out));
  D_Flip_Flop #(.trigger("rising")) d_ff_1 (
    .clk(CLK_out), .Q(d_ff_1_q), .preset(and_1_out), .reset(CLR));  // open: D, Qn, en
  and and_1 (and_1_out, in_3, Load);
  and and_2 (and_2_out, in_4, Load);
  D_Flip_Flop #(.trigger("rising")) d_ff_2 (
    .clk(CLK_out), .D(d_ff_1_q), .Q(d_ff_2_q), .preset(and_2_out), .reset(CLR));  // open: Qn, en
  and and_3 (and_3_out, in_5, Load);
  D_Flip_Flop #(.trigger("rising")) d_ff_3 (
    .clk(CLK_out), .D(d_ff_2_q), .Q(d_ff_3_q), .preset(and_3_out), .reset(CLR));  // open: Qn, en
  and and_4 (and_4_out, in_6, Load);
  D_Flip_Flop #(.trigger("rising")) d_ff_4 (
    .clk(CLK_out), .D(d_ff_5_q), .Q(out_8), .preset(and_5_out), .reset(CLR));  // open: Qn, en
  D_Flip_Flop #(.trigger("rising")) d_ff_5 (
    .clk(CLK_out), .D(d_ff_3_q), .Q(d_ff_5_q), .preset(and_4_out), .reset(CLR));  // open: Qn, en
  and and_5 (and_5_out, in_7, Load);

  // Notes on the sheet:
  //   Matrícula:405782
  //   Nome: Alan Diniz Nogueira Machado
  //   Guia 12_02 - conversor paralelo-serie com 5 bits
endmodule
