// Logisim project G12E3.circ as structural Verilog: 1 circuit, main circuit main
module main (
  input  Reset
);

  wire j_k_ff_2_q, j_k_ff_3_q, not_1_out, not_2_out, not_3_out, not_4_out, not_5_out, not_6_out, not_7_out,
       not_8_out, not_9_out, Pulso_out;

  not not_1 (not_1_out, Pulso_out);
  Clock #(.highDuration(1), .lowDuration(1)) Pulso (.out(Pulso_out));
  J_K_Flip_Flop #(.trigger("rising")) j_k_ff_1 (
    .J(1'b1), .clk(not_4_out), .K(1'b1), .preset(not_2_out), .reset(not_3_out));  // open: Q, Qn, en
  not not_2 (not_2_out, 1'b1);
  not not_3 (not_3_out, Reset);
  not not_4 (not_4_out, j_k_ff_2_q);
  J_K_Flip_Flop #(.trigger("rising")) j_k_ff_2 (
    .J(1'b1), .clk(not_7_out), .K(1'b1), .Q(j_k_ff_2_q), .preset(not_5_out), .reset(not_6_out));  // open: Qn, en
  not not_5 (not_5_out, 1'b1);
  not not_6 (not_6_out, Reset);
  not not_7 (not_7_out, j_k_ff_3_q);
  J_K_Flip_Flop #(.trigger("rising")) j_k_ff_3 (
    .J(1'b1), .clk(not_1_out), .K(1'b1), .Q(j_k_ff_3_q), .preset(not_8_out), .reset(not_9_out));  // open: Qn, en
  not not_8 (not_8_out, 1'b1);
  not not_9 (not_9_out, Reset);

  // Notes on the sheet:
  //   Matrícula:405782
  //   Nome: Alan Diniz Nogueira Machado
  //   Guia 12_03 - contador de pulsos crescente
endmodule
