// Logisim project Guia12.circ as structural Verilog: 5 circuits, main circuit Shift Register Right
module Shift_Register_Right (
  input  DATA,
  input  CLR,
  output A,
  output B,
  output C,
  output D,
  output E
);

  wire CLK_out;

  Clock #(.highDuration(1), .lowDuration(1)) CLK (.out(CLK_out));
  D_Flip_Flop #(.trigger("rising")) d_ff_1 (.clk(CLK_out), .D(DATA), .Q(A), .reset(CLR));  // open: Qn, preset, en
  D_Flip_Flop #(.trigger("rising")) d_ff_2 (.clk(CLK_out), .D(A), .Q(B), .reset(CLR));  // open: Qn, preset, en
  D_Flip_Flop #(.trigger("rising")) d_ff_3 (.clk(CLK_out), .D(B), .Q(C), .reset(CLR));  // open: Qn, preset, en
  D_Flip_Flop #(.trigger("rising")) d_ff_4 (.clk(CLK_out), .D(C), .Q(D), .reset(CLR));  // open: Qn, preset, en
  D_Flip_Flop #(.trigger("rising")) d_ff_5 (.clk(CLK_out), .D(D), .Q(E), .reset(CLR));  // open: Qn, preset, en

  // Notes on the sheet:
  //   Nome: Daniel Sathler Silva
  //   Mat: 405795
endmodule

module Parallel_Serial (
  input  CLR,
  input  LD,
  input  d4,
  input  d3,
  input  d2,
  input  d1,
  input  d0,
  output A,
  output B,
  output C,
  output D,
  output E
);

  wire and_1_out, and_2_out, and_3_out, and_4_out, and_5_out, CLK_out;

  Clock #(.highDuration(1), .lowDuration(1)) CLK (.out(CLK_out));
  and and_1 (and_1_out, LD, d4);
  D_Flip_Flop #(.trigger("rising")) d_ff_1 (
    .clk(CLK_out), .D(1'b0), .Q(A), .preset(and_1_out), .reset(CLR));  // open: Qn, en
  and and_2 (and_2_out, LD, d3);
  D_Flip_Flop #(.trigger("rising")) d_ff_2 (
    .clk(CLK_out), .D(A), .Q(B), .preset(and_2_out), .reset(CLR));  // open: Qn, en
  D_Flip_Flop #(.trigger("rising")) d_ff_3 (
    .clk(CLK_out), .D(B), .Q(C), .preset(and_3_out), .reset(CLR));  // open: Qn, en
  and and_3 (and_3_out, LD, d2);
  D_Flip_Flop #(.trigger("rising")) d_ff_4 (
    .clk(CLK_out), .D(C), .Q(D), .preset(and_4_out), .reset(CLR));  // open: Qn, en
  and and_4 (and_4_out, LD, d1);
  D_Flip_Flop #(.trigger("rising")) d_ff_5 (
    .clk(CLK_out), .D(D), .Q(E), .preset(and_5_out), .reset(CLR));  // open: Qn, en
  and and_5 (and_5_out, LD, d0);

  // Notes on the sheet:
  //   Nome: Daniel Sathler Silva
  //   Mat: 405795
endmodule

module Up_Counter (
  input  CLR,
  output A,
  output B,
  output C
);

  wire CLK_out, j_k_ff_2_q, j_k_ff_3_q;

  Clock #(.highDuration(1), .lowDuration(1)) CLK (.out(CLK_out));
  J_K_Flip_Flop #(.trigger("rising")) j_k_ff_1 (
    .J(1'b1), .clk(j_k_ff_2_q), .K(1'b1), .Qn(A), .reset(CLR));  // open: Q, preset, en
  J_K_Flip_Flop #(.trigger("rising")) j_k_ff_2 (
    .J(1'b1), .clk(j_k_ff_3_q), .K(1'b1), .Q(j_k_ff_2_q), .Qn(B), .reset(CLR));  // open: preset, en
  J_K_Flip_Flop #(.trigger("rising")) j_k_ff_3 (
    .J(1'b1), .clk(CLK_out), .K(1'b1), .Q(j_k_ff_3_q), .Qn(C), .reset(CLR));  // open: preset, en

  // Notes on the sheet:
  //   Mat: 405795
  //   Nome: Daniel Sathler Silva
endmodule

module Shift_Register_Left (
  input  DATA,
  input  CLR,
  output A,
  output B,
  output C,
  output D,
  output E
);

  wire CLK_out;

  Clock #(.highDuration(1), .lowDuration(1)) CLK (.out(CLK_out));
  D_Flip_Flop #(.trigger("rising")) d_ff_1 (.clk(CLK_out), .D(B), .Q(A), .reset(CLR));  // open: Qn, preset, en
  D_Flip_Flop #(.trigger("rising")) d_ff_2 (.clk(CLK_out), .D(C), .Q(B), .reset(CLR));  // open: Qn, preset, en
  D_Flip_Flop #(.trigger("rising")) d_ff_3 (.clk(CLK_out), .D(D), .Q(C), .reset(CLR));  // open: Qn, preset, en
  D_Flip_Flop #(.trigger("rising")) d_ff_4 (.clk(CLK_out), .D(E), .Q(D), .reset(CLR));  // open: Qn, preset, en
  D_Flip_Flop #(.trigger("rising")) d_ff_5 (.clk(CLK_out), .D(DATA), .Q(E), .reset(CLR));  // open: Qn, preset, en

  // Notes on the sheet:
  //   Nome: Daniel Sathler Silva
  //   Mat: 405795
endmodule

module Down_Counter (
  input  CLR,
  output A,
  output B,
  output C
);

  wire CLK_out;

  Clock #(.highDuration(1), .lowDuration(1)) CLK (.out(CLK_out));
  J_K_Flip_Flop #(.trigger("rising")) j_k_ff_1 (
    .J(1'b1), .clk(B), .K(1'b1), .Qn(A), .reset(CLR));  // open: Q, preset, en
  J_K_Flip_Flop #(.trigger("rising")) j_k_ff_2 (
    .J(1'b1), .clk(C), .K(1'b1), .Qn(B), .reset(CLR));  // open: Q, preset, en
  J_K_Flip_Flop #(.trigger("rising")) j_k_ff_3 (
    .J(1'b1), .clk(CLK_out), .K(1'b1), .Qn(C), .reset(CLR));  // open: Q, preset, en

  // Notes on the sheet:
  //   Mat: 405795
  //   Nome: Daniel Sathler Silva
endmodule
