// Logisim project Guia12.circ as structural Verilog
module Shift_Register___Right (
  input  DATA,
  input  CLR,
  input  DATA_2,
  input  CLR_2,
  output A,
  output B,
  output C,
  output D,
  output E,
  output out_10,
  output out_11,
  output out_12,
  output out_13,
  output out_14
);

  wire CLK_2_out, CLK_out, j_k_ff_1_qn, j_k_ff_2_qn, j_k_ff_3_qn, j_k_ff_4_qn, not_1_out;

  Clock #(.highDuration(1), .lowDuration(1)) CLK (.out(CLK_out));
  Clock #(.highDuration(1), .lowDuration(1)) CLK_2 (.out(CLK_2_out));
  not not_1 (not_1_out, DATA_2);
  D_Flip_Flop #(.trigger("rising")) d_ff_1 (.clk(CLK_out), .D(DATA), .Q(A), .reset(CLR));  // open: Qn, preset, en
  J_K_Flip_Flop #(.trigger("rising")) j_k_ff_1 (
    .J(DATA_2), .clk(CLK_2_out), .K(not_1_out), .Q(out_10), .Qn(j_k_ff_1_qn), .reset(CLR_2));  // open: preset, en
  D_Flip_Flop #(.trigger("rising")) d_ff_2 (.clk(CLK_out), .D(A), .Q(B), .reset(CLR));  // open: Qn, preset, en
  J_K_Flip_Flop #(.trigger("rising")) j_k_ff_2 (
    .J(out_10), .clk(CLK_2_out), .K(j_k_ff_1_qn), .Q(out_11), .Qn(j_k_ff_2_qn), .reset(CLR_2));  // open: preset, en
  D_Flip_Flop #(.trigger("rising")) d_ff_3 (.clk(CLK_out), .D(B), .Q(C), .reset(CLR));  // open: Qn, preset, en
  J_K_Flip_Flop #(.trigger("rising")) j_k_ff_3 (
    .J(out_11), .clk(CLK_2_out), .K(j_k_ff_2_qn), .Q(out_12), .Qn(j_k_ff_3_qn), .reset(CLR_2));  // open: preset, en
  D_Flip_Flop #(.trigger("rising")) d_ff_4 (.clk(CLK_out), .D(C), .Q(D), .reset(CLR));  // open: Qn, preset, en
  J_K_Flip_Flop #(.trigger("rising")) j_k_ff_4 (
    .J(out_12), .clk(CLK_2_out), .K(j_k_ff_3_qn), .Q(out_13), .Qn(j_k_ff_4_qn), .reset(CLR_2));  // open: preset, en
  D_Flip_Flop #(.trigger("rising")) d_ff_5 (.clk(CLK_out), .D(D), .Q(E), .reset(CLR));  // open: Qn, preset, en
  J_K_Flip_Flop #(.trigger("rising")) j_k_ff_5 (
    .J(out_13), .clk(CLK_2_out), .K(j_k_ff_4_qn), .Q(out_14), .reset(CLR_2));  // open: Qn, preset, en

  // Notes on the sheet:
  //   Matricula: 405804
  //   Nome: Gustavo Guimarães
  //   Flip-Flop D
  //   Flip-Flip JK
endmodule

module Conversor_PISO (
  input  CLR,
  input  LOAD,
  input  D5,
  input  D4,
  input  D3,
  input  D2,
  input  D1,
  output A,
  output B,
  output C,
  output D,
  output E
);

  wire and_1_out, and_2_out, and_3_out, and_4_out, and_5_out, CLK_out;

  Clock #(.highDuration(1), .lowDuration(1)) CLK (.out(CLK_out));
  and and_1 (and_1_out, LOAD, D5);
  D_Flip_Flop #(.trigger("rising")) d_ff_1 (
    .clk(CLK_out), .D(1'b0), .Q(A), .preset(and_1_out), .reset(CLR));  // open: Qn, en
  and and_2 (and_2_out, LOAD, D4);
  D_Flip_Flop #(.trigger("rising")) d_ff_2 (
    .clk(CLK_out), .D(A), .Q(B), .preset(and_2_out), .reset(CLR));  // open: Qn, en
  D_Flip_Flop #(.trigger("rising")) d_ff_3 (
    .clk(CLK_out), .D(B), .Q(C), .preset(and_3_out), .reset(CLR));  // open: Qn, en
  and and_3 (and_3_out, LOAD, D3);
  D_Flip_Flop #(.trigger("rising")) d_ff_4 (
    .clk(CLK_out), .D(C), .Q(D), .preset(and_4_out), .reset(CLR));  // open: Qn, en
  and and_4 (and_4_out, LOAD, D2);
  D_Flip_Flop #(.trigger("rising")) d_ff_5 (
    .clk(CLK_out), .D(D), .Q(E), .preset(and_5_out), .reset(CLR));  // open: Qn, en
  and and_5 (and_5_out, LOAD, D1);

  // Notes on the sheet:
  //   Matricula: 405804
  //   Nome: Gustavo Guimarães
endmodule

module Contador_Pulso_Crescente (
  input  PULSO,
  input  CLR,
  output A,
  output B,
  output C
);

  wire j_k_ff_2_q, j_k_ff_3_q;

  J_K_Flip_Flop #(.trigger("rising")) j_k_ff_1 (
    .J(1'b1), .clk(j_k_ff_2_q), .K(1'b1), .Qn(A), .reset(CLR));  // open: Q, preset, en
  J_K_Flip_Flop #(.trigger("rising")) j_k_ff_2 (
    .J(1'b1), .clk(j_k_ff_3_q), .K(1'b1), .Q(j_k_ff_2_q), .Qn(B), .reset(CLR));  // open: preset, en
  J_K_Flip_Flop #(.trigger("rising")) j_k_ff_3 (
    .J(1'b1), .clk(PULSO), .K(1'b1), .Q(j_k_ff_3_q), .Qn(C), .reset(CLR));  // open: preset, en

  // Notes on the sheet:
  //   Matricula: 405804
  //   Nome: Gustavo Guimarães
endmodule

module Shift_Register___Left (
  input  DATA,
  input  CLR,
  output A,
  output B,
  output C,
  output D,
  output E
);

  wire CLK_out;

  Clock #(.highDuration(1), .lowDuration(1)) CLK (.out(CLK_out));
  D_Flip_Flop #(.trigger("rising")) d_ff_1 (.clk(CLK_out), .D(B), .Q(A), .reset(CLR));  // open: Qn, preset, en
  D_Flip_Flop #(.trigger("rising")) d_ff_2 (.clk(CLK_out), .D(C), .Q(B), .reset(CLR));  // open: Qn, preset, en
  D_Flip_Flop #(.trigger("rising")) d_ff_3 (.clk(CLK_out), .D(D), .Q(C), .reset(CLR));  // open: Qn, preset, en
  D_Flip_Flop #(.trigger("rising")) d_ff_4 (.clk(CLK_out), .D(E), .Q(D), .reset(CLR));  // open: Qn, preset, en
  D_Flip_Flop #(.trigger("rising")) d_ff_5 (.clk(CLK_out), .D(DATA), .Q(E), .reset(CLR));  // open: Qn, preset, en

  // Notes on the sheet:
  //   Matricula: 405804
  //   Nome: Gustavo Guimarães
endmodule

module Contador_de_Pulso_Decrescente (
  input  PULSO,
  input  CLR,
  output A,
  output B,
  output C
);

  J_K_Flip_Flop #(.trigger("rising")) j_k_ff_1 (
    .J(1'b1), .clk(B), .K(1'b1), .Qn(A), .reset(CLR));  // open: Q, preset, en
  J_K_Flip_Flop #(.trigger("rising")) j_k_ff_2 (
    .J(1'b1), .clk(C), .K(1'b1), .Qn(B), .reset(CLR));  // open: Q, preset, en
  J_K_Flip_Flop #(.trigger("rising")) j_k_ff_3 (
    .J(1'b1), .clk(PULSO), .K(1'b1), .Qn(C), .reset(CLR));  // open: Q, preset, en

  // Notes on the sheet:
  //   Matricula: 405804
  //   Nome: Gustavo Guimarães
endmodule
