// Logisim project guia_12.circ as structural Verilog: 5 circuits, main circuit ex_01
module ex_01 (
  input  Clear,
  input  data,
  output out_3,
  output out_4,
  output out_5,
  output out_6,
  output out_7
);

  wire clock_1_out;

  Clock #(.highDuration(1), .lowDuration(1)) clock_1 (.out(clock_1_out));
  D_Flip_Flop #(.trigger("rising")) d_ff_1 (
    .clk(clock_1_out), .D(data), .Q(out_3), .reset(Clear));  // open: Qn, preset, en
  D_Flip_Flop #(.trigger("rising")) d_ff_2 (
    .clk(clock_1_out), .D(out_3), .Q(out_4), .reset(Clear));  // open: Qn, preset, en
  D_Flip_Flop #(.trigger("rising")) d_ff_3 (
    .clk(clock_1_out), .D(out_4), .Q(out_5), .reset(Clear));  // open: Qn, preset, en
  D_Flip_Flop #(.trigger("rising")) d_ff_4 (
    .clk(clock_1_out), .D(out_5), .Q(out_6), .reset(Clear));  // open: Qn, preset, en
  D_Flip_Flop #(.trigger("rising")) d_ff_5 (
    .clk(clock_1_out), .D(out_6), .Q(out_7), .reset(Clear));  // open: Qn, preset, en

  // Notes on the sheet:
  //   José Erimá Fernandes Júnior 4058907
endmodule

module ex_02 (
  input  Clear,
  input  data,
  input  Load,
  input  e,
  input  d,
  input  b,
  input  c,
  input  a,
  output out_9,
  output out_10,
  output out_11,
  output out_12,
  output out_13
);

  wire and_1_out, and_2_out, and_3_out, and_4_out, and_5_out, clock_1_out;

  Clock #(.highDuration(1), .lowDuration(1)) clock_1 (.out(clock_1_out));
  and and_1 (and_1_out, Load, e);
  D_Flip_Flop #(.trigger("rising")) d_ff_1 (
    .clk(clock_1_out), .D(data), .Q(out_9), .preset(and_1_out), .reset(Clear));  // open: Qn, en
  D_Flip_Flop #(.trigger("rising")) d_ff_2 (
    .clk(clock_1_out), .D(out_9), .Q(out_10), .preset(and_2_out), .reset(Clear));  // open: Qn, en
  and and_2 (and_2_out, Load, d);
  D_Flip_Flop #(.trigger("rising")) d_ff_3 (
    .clk(clock_1_out), .D(out_10), .Q(out_11), .preset(and_3_out), .reset(Clear));  // open: Qn, en
  and and_3 (and_3_out, Load, b);
  D_Flip_Flop #(.trigger("rising")) d_ff_4 (
    .clk(clock_1_out), .D(out_11), .Q(out_12), .preset(and_4_out), .reset(Clear));  // open: Qn, en
  and and_4 (and_4_out, Load, c);
  and and_5 (and_5_out, Load, a);
  D_Flip_Flop #(.trigger("rising")) d_ff_5 (
    .clk(clock_1_out), .D(out_12), .Q(out_13), .preset(and_5_out), .reset(Clear));  // open: Qn, en
endmodule

module ex_03 (
  input  Clear,
  input  data,
  output out_3,
  output out_4,
  output out_5
);

  wire clock_1_out, j_k_ff_2_q, j_k_ff_3_q;

  Clock #(.highDuration(1), .lowDuration(1)) clock_1 (.out(clock_1_out));
  J_K_Flip_Flop #(.trigger("rising")) j_k_ff_1 (
    .J(data), .clk(j_k_ff_2_q), .K(data), .Qn(out_3), .reset(Clear));  // open: Q, preset, en
  J_K_Flip_Flop #(.trigger("rising")) j_k_ff_2 (
    .J(data), .clk(j_k_ff_3_q), .K(data), .Q(j_k_ff_2_q), .Qn(out_4), .reset(Clear));  // open: preset, en
  J_K_Flip_Flop #(.trigger("rising")) j_k_ff_3 (
    .J(data), .clk(clock_1_out), .K(data), .Q(j_k_ff_3_q), .Qn(out_5), .reset(Clear));  // open: preset, en
endmodule

module ex_04 (
  input  Clear,
  input  data,
  output out_3,
  output out_4,
  output out_5,
  output out_6,
  output out_7
);

  wire clock_1_out;

  Clock #(.highDuration(1), .lowDuration(1)) clock_1 (.out(clock_1_out));
  D_Flip_Flop #(.trigger("rising")) d_ff_1 (
    .clk(clock_1_out), .D(out_4), .Q(out_3), .reset(Clear));  // open: Qn, preset, en
  D_Flip_Flop #(.trigger("rising")) d_ff_2 (
    .clk(clock_1_out), .D(out_5), .Q(out_4), .reset(Clear));  // open: Qn, preset, en
  D_Flip_Flop #(.trigger("rising")) d_ff_3 (
    .clk(clock_1_out), .D(out_6), .Q(out_5), .reset(Clear));  // open: Qn, preset, en
  D_Flip_Flop #(.trigger("rising")) d_ff_4 (
    .clk(clock_1_out), .D(out_7), .Q(out_6), .reset(Clear));  // open: Qn, preset, en
  D_Flip_Flop #(.trigger("rising")) d_ff_5 (
    .clk(clock_1_out), .D(data), .Q(out_7), .reset(Clear));  // open: Qn, preset, en
endmodule

module ex_05 (
  input  Clear,
  input  data,
  output out_3,
  output out_4,
  output out_5
);

  wire clock_1_out;

  Clock #(.highDuration(1), .lowDuration(1)) clock_1 (.out(clock_1_out));
  J_K_Flip_Flop #(.trigger("rising")) j_k_ff_1 (
    .J(data), .clk(out_4), .K(data), .Qn(out_3), .reset(Clear));  // open: Q, preset, en
  J_K_Flip_Flop #(.trigger("rising")) j_k_ff_2 (
    .J(data), .clk(out_5), .K(data), .Qn(out_4), .reset(Clear));  // open: Q, preset, en
  J_K_Flip_Flop #(.trigger("rising")) j_k_ff_3 (
    .J(data), .clk(clock_1_out), .K(data), .Qn(out_5), .reset(Clear));  // open: Q, preset, en
endmodule
