// Logisim project Guia1201.circ as structural Verilog: 1 circuit, main circuit Shift_Register_ Right
module Shift_Register__Right (
  input  DADO,
  input  CLEAR,
  output a,
  output b,
  output c,
  output d,
  output e
);

  wire CLOCK_out;

  Clock #(.highDuration(1), .lowDuration(1)) CLOCK (.out(CLOCK_out));
  D_Flip_Flop #(.trigger("rising")) d_ff_1 (.clk(CLOCK_out), .D(DADO), .Q(a), .reset(CLEAR));  // open: Qn, preset, en
  D_Flip_Flop #(.trigger("rising")) d_ff_2 (.clk(CLOCK_out), .D(a), .Q(b), .reset(CLEAR));  // open: Qn, preset, en
  D_Flip_Flop #(.trigger("rising")) d_ff_3 (.clk(CLOCK_out), .D(b), .Q(c), .reset(CLEAR));  // open: Qn, preset, en
  D_Flip_Flop #(.trigger("rising")) d_ff_4 (.clk(CLOCK_out), .D(c), .Q(d));  // open: Qn, preset, en, reset
  D_Flip_Flop #(.trigger("rising")) d_ff_5 (.clk(CLOCK_out), .D(d), .Q(e));  // open: Qn, preset, en, reset

  // Notes on the sheet:
  //   Luiz Felipe Fonseca - 405817
  //   Registrador de Deslocamento para a Direita com 5 bits
endmodule
