// Logisim project Guia1202.circ as structural Verilog: 1 circuit, main circuit CoversorParaleloSerie
module CoversorParaleloSerie (
  input  a,
  input  b,
  input  c,
  input  d,
  input  e,
  input  LOAD,
  input  CLEAR,
  output s1,
  output s2,
  output s3,
  output s4,
  output s5
);

  wire and_1_out, and_2_out, and_3_out, and_4_out, and_5_out, CLOCK_out;

  Clock #(.highDuration(1), .lowDuration(1)) CLOCK (.out(CLOCK_out));
  and and_1 (and_1_out, LOAD, a);
  D_Flip_Flop #(.trigger("rising")) d_ff_1 (
    .clk(CLOCK_out), .D(1'b0), .Q(s1), .preset(and_1_out), .reset(CLEAR));  // open: Qn, en
  and and_2 (and_2_out, LOAD, b);
  D_Flip_Flop #(.trigger("rising")) d_ff_2 (
    .clk(CLOCK_out), .D(s1), .Q(s2), .preset(and_2_out), .reset(CLEAR));  // open: Qn, en
  and and_3 (and_3_out, LOAD, c);
  D_Flip_Flop #(.trigger("rising")) d_ff_3 (
    .clk(CLOCK_out), .D(s2), .Q(s3), .preset(and_3_out), .reset(CLEAR));  // open: Qn, en
  and and_4 (and_4_out, LOAD, d);
  D_Flip_Flop #(.trigger("rising")) d_ff_4 (
    .clk(CLOCK_out), .D(s3), .Q(s4), .preset(and_4_out), .reset(CLEAR));  // open: Qn, en
  and and_5 (and_5_out, LOAD, e);
  D_Flip_Flop #(.trigger("rising")) d_ff_5 (
    .clk(CLOCK_out), .D(s4), .Q(s5), .preset(and_5_out), .reset(CLEAR));  // open: Qn, en

  // Notes on the sheet:
  //   Luiz Felipe Fonseca - 405817
  //   Conversor Paralelo Série com 5 bits
endmodule
