// Logisim project Guia1203.circ as structural Verilog: 1 circuit, main circuit main
module main (
  input  Pulse,
  input  _1,
  input  Clear,
  output a,
  output b,
  output c
);

  wire j_k_ff_2_q, j_k_ff_3_q;

  J_K_Flip_Flop #(.trigger("rising")) j_k_ff_1 (
    .J(_1), .clk(j_k_ff_2_q), .K(_1), .Qn(a), .reset(Clear));  // open: Q, preset, en
  J_K_Flip_Flop #(.trigger("rising")) j_k_ff_2 (
    .J(_1), .clk(j_k_ff_3_q), .K(_1), .Q(j_k_ff_2_q), .Qn(b), .reset(Clear));  // open: preset, en
  J_K_Flip_Flop #(.trigger("rising")) j_k_ff_3 (
    .J(_1), .clk(Pulse), .K(_1), .Q(j_k_ff_3_q), .Qn(c), .reset(Clear));  // open: preset, en

  // Notes on the sheet:
  //   Luiz Felipe Fonseca - 405817
  //   Contador Crescente de 3 bits
endmodule
