// Logisim project Guia1204.circ as structural Verilog: 1 circuit, main circuit Shift_Register_Left
module Shift_Register_Left (
  input  Dado,
  input  Clear,
  output a,
  output b,
  output c,
  output d,
  output e
);

  wire Clock_out;

  Clock #(.highDuration(1), .lowDuration(1)) Clock (.out(Clock_out));
  D_Flip_Flop #(.trigger("rising")) d_ff_1 (.clk(Clock_out), .D(b), .Q(a), .reset(Clear));  // open: Qn, preset, en
  D_Flip_Flop #(.trigger("rising")) d_ff_2 (.clk(Clock_out), .D(c), .Q(b), .reset(Clear));  // open: Qn, preset, en
  D_Flip_Flop #(.trigger("rising")) d_ff_3 (.clk(Clock_out), .D(d), .Q(c), .reset(Clear));  // open: Qn, preset, en
  D_Flip_Flop #(.trigger("rising")) d_ff_4 (.clk(Clock_out), .D(e), .Q(d), .reset(Clear));  // open: Qn, preset, en
  D_Flip_Flop #(.trigger("rising")) d_ff_5 (.clk(Clock_out), .D(Dado), .Q(e));  // open: Qn, preset, en, reset

  // Notes on the sheet:
  //   Luiz Felipe Fonseca - 405817
  //   Registrador de Deslocamento para a Esquerda com 5 bits
endmodule
