// Logisim project Guia1205.circ as structural Verilog: 1 circuit, main circuit Contador_Decrescente_3bits
module Contador_Decrescente_3bits (
  input  Pulse,
  input  in_2,
  input  Clear,
  output a,
  output b,
  output c
);

  wire j_k_ff_1_q, j_k_ff_2_q;

  J_K_Flip_Flop #(.trigger("rising")) j_k_ff_1 (
    .J(in_2), .clk(Pulse), .K(in_2), .Q(j_k_ff_1_q), .Qn(a), .reset(Clear));  // open: preset, en
  J_K_Flip_Flop #(.trigger("rising")) j_k_ff_2 (
    .J(in_2), .clk(j_k_ff_1_q), .K(in_2), .Q(j_k_ff_2_q), .Qn(b), .reset(Clear));  // open: preset, en
  J_K_Flip_Flop #(.trigger("rising")) j_k_ff_3 (
    .J(in_2), .clk(j_k_ff_2_q), .K(in_2), .Qn(c), .reset(Clear));  // open: Q, preset, en

  // Notes on the sheet:
  //   Luiz Felipe Fonseca - 405817
  //   Contador Decrescente de 03 Bits
endmodule
