// Logisim project Cicuitos.circ as structural Verilog: 5 circuits, main circuit numero_01
module numero_01 (
  input  data,
  input  clear,
  output a,
  output b,
  output c,
  output d,
  output e
);

  wire clock_out;

  Clock #(.highDuration(1), .lowDuration(1)) clock (.out(clock_out));
  D_Flip_Flop #(.trigger("rising")) d_ff_1 (.clk(clock_out), .D(data), .Q(a), .reset(clear));  // open: Qn, preset, en
  D_Flip_Flop #(.trigger("rising")) d_ff_2 (.clk(clock_out), .D(a), .Q(b), .reset(clear));  // open: Qn, preset, en
  D_Flip_Flop #(.trigger("rising")) d_ff_3 (.clk(clock_out), .D(b), .Q(c), .reset(clear));  // open: Qn, preset, en
  D_Flip_Flop #(.trigger("rising")) d_ff_4 (.clk(clock_out), .D(c), .Q(d), .reset(clear));  // open: Qn, preset, en
  D_Flip_Flop #(.trigger("rising")) d_ff_5 (.clk(clock_out), .D(d), .Q(e), .reset(clear));  // open: Qn, preset, en

  // Notes on the sheet:
  //   REGISTRADOR DE DESLOCAMENTO PARA A DIREITA
endmodule

module numero_02 (
  input  clear,
  input  load,
  input  d4,
  input  d3,
  input  d2,
  input  d1,
  input  d0,
  output a,
  output b,
  output c,
  output d,
  output e
);

  wire and_1_out, and_2_out, and_3_out, and_4_out, and_5_out, clock_out;

  Clock #(.highDuration(1), .lowDuration(1)) clock (.out(clock_out));
  D_Flip_Flop #(.trigger("rising")) d_ff_1 (
    .clk(clock_out), .D(1'b0), .Q(a), .preset(and_1_out), .reset(clear));  // open: Qn, en
  and and_1 (and_1_out, load, d4);
  D_Flip_Flop #(.trigger("rising")) d_ff_2 (
    .clk(clock_out), .D(a), .Q(b), .preset(and_2_out), .reset(clear));  // open: Qn, en
  and and_2 (and_2_out, load, d3);
  D_Flip_Flop #(.trigger("rising")) d_ff_3 (
    .clk(clock_out), .D(b), .Q(c), .preset(and_3_out), .reset(clear));  // open: Qn, en
  and and_3 (and_3_out, load, d2);
  D_Flip_Flop #(.trigger("rising")) d_ff_4 (
    .clk(clock_out), .D(c), .Q(d), .preset(and_4_out), .reset(clear));  // open: Qn, en
  and and_4 (and_4_out, load, d1);
  D_Flip_Flop #(.trigger("rising")) d_ff_5 (
    .clk(clock_out), .D(d), .Q(e), .preset(and_5_out), .reset(clear));  // open: Qn, en
  and and_5 (and_5_out, load, d0);

  // Notes on the sheet:
  //   CONVERSOR PARALELO-SERIE
endmodule

module numero_03 (
  input  _1,
  input  clear,
  output a,
  output b,
  output c
);

  wire j_k_ff_2_q, j_k_ff_3_q, pulse_out;

  Clock #(.highDuration(1), .lowDuration(1)) pulse (.out(pulse_out));
  J_K_Flip_Flop #(.trigger("rising")) j_k_ff_1 (
    .J(_1), .clk(j_k_ff_2_q), .K(_1), .Qn(a), .reset(clear));  // open: Q, preset, en
  J_K_Flip_Flop #(.trigger("rising")) j_k_ff_2 (
    .J(_1), .clk(j_k_ff_3_q), .K(_1), .Q(j_k_ff_2_q), .Qn(b), .reset(clear));  // open: preset, en
  J_K_Flip_Flop #(.trigger("rising")) j_k_ff_3 (
    .J(_1), .clk(pulse_out), .K(_1), .Q(j_k_ff_3_q), .Qn(c), .reset(clear));  // open: preset, en

  // Notes on the sheet:
  //   CONTADOR DE PULSOS CRESCENTE
endmodule

module numero_04 (
  input  data,
  input  clear,
  output a,
  output b,
  output c,
  output d,
  output e
);

  wire clock_out;

  Clock #(.highDuration(1), .lowDuration(1)) clock (.out(clock_out));
  D_Flip_Flop #(.trigger("rising")) d_ff_1 (.clk(clock_out), .D(b), .Q(a), .reset(clear));  // open: Qn, preset, en
  D_Flip_Flop #(.trigger("rising")) d_ff_2 (.clk(clock_out), .D(c), .Q(b), .reset(clear));  // open: Qn, preset, en
  D_Flip_Flop #(.trigger("rising")) d_ff_3 (.clk(clock_out), .D(d), .Q(c), .reset(clear));  // open: Qn, preset, en
  D_Flip_Flop #(.trigger("rising")) d_ff_4 (.clk(clock_out), .D(e), .Q(d), .reset(clear));  // open: Qn, preset, en
  D_Flip_Flop #(.trigger("rising")) d_ff_5 (.clk(clock_out), .D(data), .Q(e), .reset(clear));  // open: Qn, preset, en

  // Notes on the sheet:
  //   REGISTRADOR DE DESLOCAMENTO PARA A ESQUERDA
endmodule

module numero_05 (
  input  _1,
  input  clear,
  output a,
  output b,
  output c
);

  wire pulse_out;

  Clock #(.highDuration(1), .lowDuration(1)) pulse (.out(pulse_out));
  J_K_Flip_Flop #(.trigger("rising")) j_k_ff_1 (.J(_1), .clk(b), .K(_1), .Qn(a), .reset(clear));  // open: Q, preset, en
  J_K_Flip_Flop #(.trigger("rising")) j_k_ff_2 (.J(_1), .clk(c), .K(_1), .Qn(b), .reset(clear));  // open: Q, preset, en
  J_K_Flip_Flop #(.trigger("rising")) j_k_ff_3 (
    .J(_1), .clk(pulse_out), .K(_1), .Qn(c), .reset(clear));  // open: Q, preset, en

  // Notes on the sheet:
  //   CONTADOR DE PULSOS DECRESCENTE
endmodule
