// Logisim project implementacao02.circ as structural Verilog: 1 circuit, main circuit main
module main (
  input  Data,
  input  Clear,
  input  Load,
  input  e,
  input  d,
  input  c,
  input  b,
  input  a,
  output [4:0] out_9
);

  wire and_1_out, and_2_out, and_3_out, and_4_out, and_5_out, Clock_out;

  Clock #(.highDuration(1), .lowDuration(1)) Clock (.out(Clock_out));
  and and_1 (and_1_out, Load, e);
  D_Flip_Flop #(.trigger("rising")) d_ff_1 (
    .clk(Clock_out), .D(Data), .Q(out_9[4]), .preset(and_1_out), .reset(Clear));  // open: Qn, en
  D_Flip_Flop #(.trigger("rising")) d_ff_2 (
    .clk(Clock_out), .D(out_9[4]), .Q(out_9[3]), .preset(and_2_out), .reset(Clear));  // open: Qn, en
  and and_2 (and_2_out, Load, d);
  and and_3 (and_3_out, Load, c);
  D_Flip_Flop #(.trigger("rising")) d_ff_3 (
    .clk(Clock_out), .D(out_9[3]), .Q(out_9[2]), .preset(and_3_out), .reset(Clear));  // open: Qn, en
  D_Flip_Flop #(.trigger("rising")) d_ff_4 (
    .clk(Clock_out), .D(out_9[2]), .Q(out_9[1]), .preset(and_4_out), .reset(Clear));  // open: Qn, en
  and and_4 (and_4_out, Load, b);
  and and_5 (and_5_out, Load, a);
  D_Flip_Flop #(.trigger("rising")) d_ff_5 (
    .clk(Clock_out), .D(out_9[1]), .Q(out_9[0]), .preset(and_5_out), .reset(Clear));  // open: Qn, en

  // Notes on the sheet:
  //   Arquitetura de Computadores - Guia 12
  //   Conversor paralelo-serie com 5bits
  //   Tiago Menegaz de Melo Garcia           405844
endmodule
