// Logisim project implementacao03.circ as structural Verilog: 1 circuit, main circuit main
module main (
  input  Data,
  input  Clear,
  output out_3,
  output out_4,
  output out_5,
  output out_6,
  output out_7
);

  wire Clock_out, t_ff_1_qn, t_ff_2_qn, t_ff_3_qn, t_ff_4_qn;

  Clock #(.highDuration(1), .lowDuration(1)) Clock (.out(Clock_out));
  T_Flip_Flop #(.trigger("rising")) t_ff_1 (
    .clk(Clock_out), .T(Data), .Q(out_7), .Qn(t_ff_1_qn), .reset(Clear));  // open: preset, en
  T_Flip_Flop #(.trigger("rising")) t_ff_2 (
    .clk(t_ff_1_qn), .T(t_ff_1_qn), .Q(out_6), .Qn(t_ff_2_qn), .reset(Clear));  // open: preset, en
  T_Flip_Flop #(.trigger("rising")) t_ff_3 (
    .clk(t_ff_2_qn), .T(t_ff_2_qn), .Q(out_5), .Qn(t_ff_3_qn), .reset(Clear));  // open: preset, en
  T_Flip_Flop #(.trigger("rising")) t_ff_4 (
    .clk(t_ff_3_qn), .T(t_ff_3_qn), .Q(out_4), .Qn(t_ff_4_qn), .reset(Clear));  // open: preset, en
  T_Flip_Flop #(.trigger("rising")) t_ff_5 (
    .clk(t_ff_4_qn), .T(t_ff_4_qn), .Q(out_3), .reset(Clear));  // open: Qn, preset, en

  // Notes on the sheet:
  //   Arquitetura de Computadores - Guia 12
  //   Contador de pulsos crescente de 5 bits
  //   Tiago Menegaz de Melo Garcia              405844
endmodule
