// Logisim project implementacao04.circ as structural Verilog: 1 circuit, main circuit main
module main (
  input  Data,
  input  Clear,
  output [4:0] out_3
);

  wire Clock_out, j_k_ff_1_qn, j_k_ff_2_qn, j_k_ff_3_qn, j_k_ff_4_qn, not_1_out, or_1_out;

  Clock #(.highDuration(1), .lowDuration(1)) Clock (.out(Clock_out));
  or or_1 (or_1_out, Data, out_3[4]);
  not not_1 (not_1_out, Data);
  J_K_Flip_Flop #(.trigger("rising")) j_k_ff_1 (
    .J(or_1_out), .clk(Clock_out), .K(not_1_out), .Q(out_3[0]), .Qn(j_k_ff_1_qn), .reset(Clear));  // open: preset, en
  J_K_Flip_Flop #(.trigger("rising")) j_k_ff_2 (
    .J(out_3[0]), .clk(Clock_out), .K(j_k_ff_1_qn), .Q(out_3[1]), .Qn(j_k_ff_2_qn), .reset(Clear));  // open: preset, en
  J_K_Flip_Flop #(.trigger("rising")) j_k_ff_3 (
    .J(out_3[1]), .clk(Clock_out), .K(j_k_ff_2_qn), .Q(out_3[2]), .Qn(j_k_ff_3_qn), .reset(Clear));  // open: preset, en
  J_K_Flip_Flop #(.trigger("rising")) j_k_ff_4 (
    .J(out_3[2]), .clk(Clock_out), .K(j_k_ff_3_qn), .Q(out_3[3]), .Qn(j_k_ff_4_qn), .reset(Clear));  // open: preset, en
  J_K_Flip_Flop #(.trigger("rising")) j_k_ff_5 (
    .J(out_3[3]), .clk(Clock_out), .K(j_k_ff_4_qn), .Q(out_3[4]), .reset(Clear));  // open: Qn, preset, en

  // Notes on the sheet:
  //   Arquitetura de Computadores - Guia 12
  //   Registrador de deslocamento para esquerda com 5 bits
  //   Tiago Menegaz de Melo Garcia          405844
endmodule
