// Logisim project implementacao05.circ as structural Verilog: 1 circuit, main circuit main
module main (
  input  Data,
  input  Clear,
  output [4:0] out_3
);

  wire Clock_out;

  Clock #(.highDuration(1), .lowDuration(1)) Clock (.out(Clock_out));
  J_K_Flip_Flop #(.trigger("rising")) j_k_ff_1 (
    .J(Data), .clk(Clock_out), .K(Data), .Q(out_3[0]), .reset(Clear));  // open: Qn, preset, en
  J_K_Flip_Flop #(.trigger("rising")) j_k_ff_2 (
    .J(Data), .clk(out_3[0]), .K(Data), .Q(out_3[1]), .reset(Clear));  // open: Qn, preset, en
  J_K_Flip_Flop #(.trigger("rising")) j_k_ff_3 (
    .J(Data), .clk(out_3[1]), .K(Data), .Q(out_3[2]), .reset(Clear));  // open: Qn, preset, en
  J_K_Flip_Flop #(.trigger("rising")) j_k_ff_4 (
    .J(Data), .clk(out_3[2]), .K(Data), .Q(out_3[3]), .reset(Clear));  // open: Qn, preset, en
  J_K_Flip_Flop #(.trigger("rising")) j_k_ff_5 (
    .J(Data), .clk(out_3[3]), .K(Data), .Q(out_3[4]), .reset(Clear));  // open: Qn, preset, en

  // Notes on the sheet:
  //   Arquitetura de Computadores - Guia 12
  //   Contador de pulsos decrescente de 5 bits
  //   Tiago Menegaz de Melo Garcia              405844
endmodule
