// Logisim project Exercicio02.circ as structural Verilog: 1 circuit, main circuit main
module main (
  input  Clear,
  input  Load,
  input  [4:0] Data_In,
  output Data_Out
);

  wire and_1_out, and_2_out, and_3_out, and_4_out, and_5_out, clock_1_out, j_k_ff_1_q, j_k_ff_1_qn,
       j_k_ff_2_q, j_k_ff_2_qn, j_k_ff_3_q, j_k_ff_3_qn, j_k_ff_4_q, j_k_ff_4_qn;

  Clock #(.highDuration(1), .lowDuration(1)) clock_1 (.out(clock_1_out));
  J_K_Flip_Flop #(.trigger("rising")) j_k_ff_1 (
    .J(1'b0), .clk(clock_1_out), .K(1'b1), .Q(j_k_ff_1_q), .Qn(j_k_ff_1_qn), .preset(and_1_out), .reset(Clear));  // open: en
  and and_1 (and_1_out, Data_In[4], Load);
  J_K_Flip_Flop #(.trigger("rising")) j_k_ff_2 (
    .J(j_k_ff_1_q), .clk(clock_1_out), .K(j_k_ff_1_qn), .Q(j_k_ff_2_q), .Qn(j_k_ff_2_qn), .preset(and_2_out),
    .reset(Clear));  // open: en
  and and_2 (and_2_out, Data_In[3], Load);
  J_K_Flip_Flop #(.trigger("rising")) j_k_ff_3 (
    .J(j_k_ff_2_q), .clk(clock_1_out), .K(j_k_ff_2_qn), .Q(j_k_ff_3_q), .Qn(j_k_ff_3_qn), .preset(and_3_out),
    .reset(Clear));  // open: en
  and and_3 (and_3_out, Data_In[2], Load);
  J_K_Flip_Flop #(.trigger("rising")) j_k_ff_4 (
    .J(j_k_ff_3_q), .clk(clock_1_out), .K(j_k_ff_3_qn), .Q(j_k_ff_4_q), .Qn(j_k_ff_4_qn), .preset(and_4_out),
    .reset(Clear));  // open: en
  and and_4 (and_4_out, Data_In[1], Load);
  J_K_Flip_Flop #(.trigger("rising")) j_k_ff_5 (
    .J(j_k_ff_4_q), .clk(clock_1_out), .K(j_k_ff_4_qn), .Q(Data_Out), .preset(and_5_out), .reset(Clear));  // open: Qn, en
  and and_5 (and_5_out, Data_In[0], Load);

  // Notes on the sheet:
  //   Parallel to Serial Converter
endmodule
