// Logisim project Exercicio03.circ as structural Verilog: 1 circuit, main circuit main
module main (
  input  Reset
);

  wire clock_1_out, j_k_ff_2_q, j_k_ff_3_q, not_1_out, not_2_out, not_3_out, not_4_out, not_5_out, not_6_out;

  not not_1 (not_1_out, j_k_ff_2_q);
  not not_2 (not_2_out, 1'b1);
  Clock #(.highDuration(1), .lowDuration(1)) clock_1 (.out(clock_1_out));
  J_K_Flip_Flop #(.trigger("rising")) j_k_ff_1 (
    .J(1'b1), .clk(not_1_out), .K(1'b1), .preset(not_2_out), .reset(Reset));  // open: Q, Qn, en
  not not_3 (not_3_out, j_k_ff_3_q);
  J_K_Flip_Flop #(.trigger("rising")) j_k_ff_2 (
    .J(1'b1), .clk(not_3_out), .K(1'b1), .Q(j_k_ff_2_q), .preset(not_4_out), .reset(Reset));  // open: Qn, en
  not not_4 (not_4_out, 1'b1);
  J_K_Flip_Flop #(.trigger("rising")) j_k_ff_3 (
    .J(1'b1), .clk(not_5_out), .K(1'b1), .Q(j_k_ff_3_q), .preset(not_6_out), .reset(Reset));  // open: Qn, en
  not not_5 (not_5_out, clock_1_out);
  not not_6 (not_6_out, 1'b1);

  // Notes on the sheet:
  //   Crescent Pulse Counter
endmodule
