// Logisim project Exercicio04.circ as structural Verilog: 1 circuit, main circuit main
module main (
  input  Entrada,
  input  Clear,
  output Saida
);

  wire Clk_out, j_k_ff_2_q, j_k_ff_2_qn, j_k_ff_3_q, j_k_ff_3_qn, j_k_ff_4_q, j_k_ff_4_qn, j_k_ff_5_q,
       j_k_ff_5_qn;

  Clock #(.highDuration(1), .lowDuration(1)) Clk (.out(Clk_out));
  J_K_Flip_Flop #(.trigger("rising")) j_k_ff_1 (
    .J(j_k_ff_2_q), .clk(Clk_out), .K(j_k_ff_2_qn), .Q(Saida), .reset(Clear));  // open: Qn, preset, en
  J_K_Flip_Flop #(.trigger("rising")) j_k_ff_2 (
    .J(j_k_ff_3_q), .clk(Clk_out), .K(j_k_ff_3_qn), .Q(j_k_ff_2_q), .Qn(j_k_ff_2_qn), .reset(Clear));  // open: preset, en
  J_K_Flip_Flop #(.trigger("rising")) j_k_ff_3 (
    .J(j_k_ff_4_q), .clk(Clk_out), .K(j_k_ff_4_qn), .Q(j_k_ff_3_q), .Qn(j_k_ff_3_qn), .reset(Clear));  // open: preset, en
  J_K_Flip_Flop #(.trigger("rising")) j_k_ff_4 (
    .J(j_k_ff_5_q), .clk(Clk_out), .K(j_k_ff_5_qn), .Q(j_k_ff_4_q), .Qn(j_k_ff_4_qn), .reset(Clear));  // open: preset, en
  J_K_Flip_Flop #(.trigger("rising")) j_k_ff_5 (
    .J(Entrada), .clk(Clk_out), .K(Entrada), .Q(j_k_ff_5_q), .Qn(j_k_ff_5_qn), .reset(Clear));  // open: preset, en

  // Notes on the sheet:
  //   Shift Register Left
endmodule
