// Logisim project Exercicio05.circ as structural Verilog: 1 circuit, main circuit main
module main (
  input  Reset
);

  wire clock_1_out, j_k_ff_2_q, j_k_ff_3_q;

  Clock #(.highDuration(1), .lowDuration(1)) clock_1 (.out(clock_1_out));
  J_K_Flip_Flop #(.trigger("rising")) j_k_ff_1 (
    .J(1'b1), .clk(j_k_ff_2_q), .K(1'b1), .reset(Reset));  // open: Q, Qn, preset, en
  J_K_Flip_Flop #(.trigger("rising")) j_k_ff_2 (
    .J(1'b1), .clk(j_k_ff_3_q), .K(1'b1), .Q(j_k_ff_2_q), .reset(Reset));  // open: Qn, preset, en
  J_K_Flip_Flop #(.trigger("rising")) j_k_ff_3 (
    .J(1'b1), .clk(clock_1_out), .K(1'b1), .Q(j_k_ff_3_q), .reset(Reset));  // open: Qn, preset, en

  // Notes on the sheet:
  //   Decrescent Pulse Counter
endmodule
