// Logisim project guia 12 - 412727.circ as structural Verilog: 6 circuits, main circuit main
module main (
);

  Exercicio_1 exercicio_1_1 ();  // open: DADO, out_2, out_3, out_4, out_5
  Exercicio_2 exercicio_2_1 ();  // open: out_5, out_6, out_7, load, d2, d1, d0
  Exercicio_3 exercicio_3_1 ();  // open: sIN, asIN, out_3, out_4, out_5, out_6, out_7, out_8
  Exercicio_4 exercicio_4_1 ();  // open: DADO, out_2, out_3, out_4, out_5, out_6
  Exercicio_5 exercicio_5_1 ();  // open: sIN, asIN, out_3, out_4, out_5, out_6, out_7, out_8

  // Notes on the sheet:
  //   Augusto Ferreira Andrade Do Carmo - 412727 - guia 12
  //   O clock não está aprecendo nas caixas
  //   EXPERIMENTE USAR UM PINO DE ENTRADA
endmodule

module Exercicio_1 (
  input  DADO,
  output out_2,
  output out_3,
  output out_4,
  output out_5
);

  wire CLK_out;

  Clock #(.highDuration(1), .lowDuration(1)) CLK (.out(CLK_out));
  D_Flip_Flop #(.trigger("rising")) d_ff_1 (.clk(CLK_out), .D(DADO), .Q(out_2));  // open: Qn, preset, en, reset
  D_Flip_Flop #(.trigger("rising")) d_ff_2 (.clk(CLK_out), .D(out_2), .Q(out_3));  // open: Qn, preset, en, reset
  D_Flip_Flop #(.trigger("rising")) d_ff_3 (.clk(CLK_out), .D(out_3), .Q(out_4));  // open: Qn, preset, en, reset
  D_Flip_Flop #(.trigger("rising")) d_ff_4 (.clk(CLK_out), .D(out_4), .Q(out_5));  // open: Qn, preset, en, reset
  D_Flip_Flop #(.trigger("rising")) d_ff_5 (.clk(CLK_out), .D(out_5));  // open: Q, Qn, preset, en, reset
endmodule

module Exercicio_3 (
  input  sIN,
  input  asIN,
  output out_3,
  output out_4,
  output out_5,
  output out_6,
  output out_7,
  output out_8
);

  wire and_1_out, and_2_out, asCLk_out, sCLK_out, t_ff_1_qn, t_ff_3_qn;

  Clock #(.highDuration(1), .lowDuration(1)) sCLK (.out(sCLK_out));
  Clock #(.highDuration(1), .lowDuration(1)) asCLk (.out(asCLk_out));
  T_Flip_Flop #(.trigger("rising")) t_ff_1 (
    .clk(sCLK_out), .T(sIN), .Q(out_5), .Qn(t_ff_1_qn));  // open: preset, reset, en
  T_Flip_Flop #(.trigger("rising")) t_ff_2 (.clk(asCLk_out), .T(asIN), .Q(out_8));  // open: Qn, preset, reset, en
  and and_1 (and_1_out, asIN, out_8);
  and and_2 (and_2_out, and_1_out, out_7);
  T_Flip_Flop #(.trigger("rising")) t_ff_3 (
    .clk(t_ff_1_qn), .T(sIN), .Q(out_4), .Qn(t_ff_3_qn));  // open: preset, reset, en
  T_Flip_Flop #(.trigger("rising")) t_ff_4 (.clk(asCLk_out), .T(and_1_out), .Q(out_7));  // open: Qn, preset, reset, en
  T_Flip_Flop #(.trigger("rising")) t_ff_5 (.clk(t_ff_3_qn), .T(sIN), .Q(out_3));  // open: Qn, preset, reset, en
  T_Flip_Flop #(.trigger("rising")) t_ff_6 (.clk(asCLk_out), .T(and_2_out), .Q(out_6));  // open: Qn, preset, reset, en

  // Notes on the sheet:
  //   Assíncrono
  //   Síncrono
endmodule

module Exercicio_4 (
  input  DADO,
  output out_2,
  output out_3,
  output out_4,
  output out_5,
  output out_6
);

  wire CLK_out;

  Clock #(.highDuration(1), .lowDuration(1)) CLK (.out(CLK_out));
  D_Flip_Flop #(.trigger("rising")) d_ff_1 (.clk(CLK_out), .D(out_3), .Q(out_2));  // open: Qn, preset, en, reset
  D_Flip_Flop #(.trigger("rising")) d_ff_2 (.clk(CLK_out), .D(out_4), .Q(out_3));  // open: Qn, preset, en, reset
  D_Flip_Flop #(.trigger("rising")) d_ff_3 (.clk(CLK_out), .D(out_5), .Q(out_4));  // open: Qn, preset, en, reset
  D_Flip_Flop #(.trigger("rising")) d_ff_4 (.clk(CLK_out), .D(out_6), .Q(out_5));  // open: Qn, preset, en, reset
  D_Flip_Flop #(.trigger("rising")) d_ff_5 (.clk(CLK_out), .D(DADO), .Q(out_6));  // open: Qn, preset, en, reset
endmodule

module Exercicio_5 (
  input  sIN,
  input  asIN,
  output out_3,
  output out_4,
  output out_5,
  output out_6,
  output out_7,
  output out_8
);

  wire and_1_out, and_2_out, asCLk_out, sCLK_out, t_ff_2_qn, t_ff_4_qn;

  Clock #(.highDuration(1), .lowDuration(1)) sCLK (.out(sCLK_out));
  Clock #(.highDuration(1), .lowDuration(1)) asCLk (.out(asCLk_out));
  T_Flip_Flop #(.trigger("rising")) t_ff_1 (.clk(sCLK_out), .T(sIN), .Q(out_5));  // open: Qn, preset, reset, en
  T_Flip_Flop #(.trigger("rising")) t_ff_2 (
    .clk(asCLk_out), .T(asIN), .Q(out_8), .Qn(t_ff_2_qn));  // open: preset, reset, en
  and and_1 (and_1_out, asIN, t_ff_2_qn);
  and and_2 (and_2_out, and_1_out, t_ff_4_qn);
  T_Flip_Flop #(.trigger("rising")) t_ff_3 (.clk(out_5), .T(sIN), .Q(out_4));  // open: Qn, preset, reset, en
  T_Flip_Flop #(.trigger("rising")) t_ff_4 (
    .clk(asCLk_out), .T(and_1_out), .Q(out_7), .Qn(t_ff_4_qn));  // open: preset, reset, en
  T_Flip_Flop #(.trigger("rising")) t_ff_5 (.clk(out_4), .T(sIN), .Q(out_3));  // open: Qn, preset, reset, en
  T_Flip_Flop #(.trigger("rising")) t_ff_6 (.clk(asCLk_out), .T(and_2_out), .Q(out_6));  // open: Qn, preset, reset, en

  // Notes on the sheet:
  //   Assíncrono
  //   Síncrono
endmodule

module Exercicio_2 (
  input  load,
  input  d0,
  input  d2,
  input  d1,
  output out_5,
  output out_6,
  output out_7
);

  wire and_1_out, and_2_out, and_3_out, CLK_out;

  Clock #(.highDuration(1), .lowDuration(1)) CLK (.out(CLK_out));
  D_Flip_Flop #(.trigger("rising")) d_ff_1 (
    .clk(CLK_out), .D(1'b0), .Q(out_5), .preset(and_1_out));  // open: Qn, en, reset
  and and_1 (and_1_out, load, d2);
  D_Flip_Flop #(.trigger("rising")) d_ff_2 (
    .clk(CLK_out), .D(out_5), .Q(out_6), .preset(and_2_out));  // open: Qn, en, reset
  and and_2 (and_2_out, load, d1);
  D_Flip_Flop #(.trigger("rising")) d_ff_3 (
    .clk(CLK_out), .D(out_6), .Q(out_7), .preset(and_3_out));  // open: Qn, en, reset
  and and_3 (and_3_out, load, d0);
endmodule
