// Logisim project Guia12.circ as structural Verilog: 6 circuits, main circuit main
module main (
);


  // Notes on the sheet:
  //   Lucas Teixeira Santos - 415383
endmodule

module Ex01 (
  input  Input,
  input  Clear,
  output [4:0] s
);

  wire Clock_out;

  Clock #(.highDuration(1), .lowDuration(1)) Clock (.out(Clock_out));
  D_Flip_Flop #(.trigger("rising")) d_ff_1 (
    .clk(Clock_out), .D(Input), .Q(s[4]), .reset(Clear));  // open: Qn, preset, en
  D_Flip_Flop #(.trigger("rising")) d_ff_2 (
    .clk(Clock_out), .D(s[4]), .Q(s[3]), .reset(Clear));  // open: Qn, preset, en
  D_Flip_Flop #(.trigger("rising")) d_ff_3 (
    .clk(Clock_out), .D(s[3]), .Q(s[2]), .reset(Clear));  // open: Qn, preset, en
  D_Flip_Flop #(.trigger("rising")) d_ff_4 (
    .clk(Clock_out), .D(s[2]), .Q(s[1]), .reset(Clear));  // open: Qn, preset, en
  D_Flip_Flop #(.trigger("rising")) d_ff_5 (
    .clk(Clock_out), .D(s[1]), .Q(s[0]), .reset(Clear));  // open: Qn, preset, en

  // Notes on the sheet:
  //   Deslocador de bits para direita
endmodule

module Ex02 (
  input  In,
  input  Clear,
  input  EnLoads,
  input  [3:0] Loads
);

  wire and_1_out, and_2_out, and_3_out, and_4_out, Clock_out, j_k_ff_1_q, j_k_ff_1_qn, j_k_ff_2_q,
       j_k_ff_2_qn, j_k_ff_3_q, j_k_ff_3_qn, not_1_out;

  Clock #(.highDuration(1), .lowDuration(1)) Clock (.out(Clock_out));
  not not_1 (not_1_out, In);
  J_K_Flip_Flop #(.trigger("rising")) j_k_ff_1 (
    .J(In), .clk(Clock_out), .K(not_1_out), .Q(j_k_ff_1_q), .Qn(j_k_ff_1_qn), .preset(and_1_out),
    .reset(Clear));  // open: en
  and and_1 (and_1_out, Loads[3], EnLoads);
  J_K_Flip_Flop #(.trigger("rising")) j_k_ff_2 (
    .J(j_k_ff_1_q), .clk(Clock_out), .K(j_k_ff_1_qn), .Q(j_k_ff_2_q), .Qn(j_k_ff_2_qn), .preset(and_2_out),
    .reset(Clear));  // open: en
  and and_2 (and_2_out, EnLoads, Loads[2]);
  J_K_Flip_Flop #(.trigger("rising")) j_k_ff_3 (
    .J(j_k_ff_2_q), .clk(Clock_out), .K(j_k_ff_2_qn), .Q(j_k_ff_3_q), .Qn(j_k_ff_3_qn), .preset(and_3_out),
    .reset(Clear));  // open: en
  and and_3 (and_3_out, Loads[1], EnLoads);
  J_K_Flip_Flop #(.trigger("rising")) j_k_ff_4 (
    .J(j_k_ff_3_q), .clk(Clock_out), .K(j_k_ff_3_qn), .preset(and_4_out), .reset(Clear));  // open: Q, Qn, en
  and and_4 (and_4_out, EnLoads, Loads[0]);

  // Notes on the sheet:
  //   Conversor Paralelo-Serie
endmodule

module Ex03 (
  input  Reset
);

  wire Clock_out, j_k_ff_2_qn, j_k_ff_3_qn;

  Clock #(.highDuration(1), .lowDuration(1)) Clock (.out(Clock_out));
  J_K_Flip_Flop #(.trigger("rising")) j_k_ff_1 (
    .J(1'b1), .clk(j_k_ff_2_qn), .K(1'b1), .reset(Reset));  // open: Q, Qn, preset, en
  J_K_Flip_Flop #(.trigger("rising")) j_k_ff_2 (
    .J(1'b1), .clk(j_k_ff_3_qn), .K(1'b1), .Qn(j_k_ff_2_qn), .reset(Reset));  // open: Q, preset, en
  J_K_Flip_Flop #(.trigger("rising")) j_k_ff_3 (
    .J(1'b1), .clk(Clock_out), .K(1'b1), .Qn(j_k_ff_3_qn), .reset(Reset));  // open: Q, preset, en

  // Notes on the sheet:
  //   Pulsos Crescentes
endmodule

module Ex04 (
  input  Input,
  input  Clear,
  output [4:0] s
);

  wire Clock_out;

  Clock #(.highDuration(1), .lowDuration(1)) Clock (.out(Clock_out));
  D_Flip_Flop #(.trigger("rising")) d_ff_1 (
    .clk(Clock_out), .D(Input), .Q(s[0]), .reset(Clear));  // open: Qn, preset, en
  D_Flip_Flop #(.trigger("rising")) d_ff_2 (
    .clk(Clock_out), .D(s[0]), .Q(s[1]), .reset(Clear));  // open: Qn, preset, en
  D_Flip_Flop #(.trigger("rising")) d_ff_3 (
    .clk(Clock_out), .D(s[1]), .Q(s[2]), .reset(Clear));  // open: Qn, preset, en
  D_Flip_Flop #(.trigger("rising")) d_ff_4 (
    .clk(Clock_out), .D(s[2]), .Q(s[3]), .reset(Clear));  // open: Qn, preset, en
  D_Flip_Flop #(.trigger("rising")) d_ff_5 (
    .clk(Clock_out), .D(s[3]), .Q(s[4]), .reset(Clear));  // open: Qn, preset, en

  // Notes on the sheet:
  //   Deslocador de bits para esquerda
endmodule

module Ex05 (
  input  Reset
);

  wire Clock_out, j_k_ff_2_q, j_k_ff_3_q;

  Clock #(.highDuration(1), .lowDuration(1)) Clock (.out(Clock_out));
  J_K_Flip_Flop #(.trigger("rising")) j_k_ff_1 (
    .J(1'b1), .clk(j_k_ff_2_q), .K(1'b1), .reset(Reset));  // open: Q, Qn, preset, en
  J_K_Flip_Flop #(.trigger("rising")) j_k_ff_2 (
    .J(1'b1), .clk(j_k_ff_3_q), .K(1'b1), .Q(j_k_ff_2_q), .reset(Reset));  // open: Qn, preset, en
  J_K_Flip_Flop #(.trigger("rising")) j_k_ff_3 (
    .J(1'b1), .clk(Clock_out), .K(1'b1), .Q(j_k_ff_3_q), .reset(Reset));  // open: Qn, preset, en

  // Notes on the sheet:
  //   Pulsos Decrescentes
endmodule
