// Logisim project Exercicio01.circ as structural Verilog: 1 circuit, main circuit main
module main (
  input  DADOS,
  input  CLEAR,
  output out_3
);

  wire CLOCK_out, d_ff_1_q, d_ff_2_q, d_ff_3_q, d_ff_4_q;

  Clock #(.highDuration(1), .lowDuration(1)) CLOCK (.out(CLOCK_out));
  D_Flip_Flop #(.trigger("rising")) d_ff_1 (
    .clk(CLOCK_out), .D(DADOS), .Q(d_ff_1_q), .reset(CLEAR));  // open: Qn, preset, en
  D_Flip_Flop #(.trigger("rising")) d_ff_2 (
    .clk(CLOCK_out), .D(d_ff_1_q), .Q(d_ff_2_q), .reset(CLEAR));  // open: Qn, preset, en
  D_Flip_Flop #(.trigger("rising")) d_ff_3 (
    .clk(CLOCK_out), .D(d_ff_2_q), .Q(d_ff_3_q), .reset(CLEAR));  // open: Qn, preset, en
  D_Flip_Flop #(.trigger("rising")) d_ff_4 (
    .clk(CLOCK_out), .D(d_ff_3_q), .Q(d_ff_4_q), .reset(CLEAR));  // open: Qn, preset, en
  D_Flip_Flop #(.trigger("rising")) d_ff_5 (
    .clk(CLOCK_out), .D(d_ff_4_q), .Q(out_3), .reset(CLEAR));  // open: Qn, preset, en

  // Notes on the sheet:
  //   Felipe Augusto Torres
endmodule
