// Logisim project Exercicio02.circ as structural Verilog: 1 circuit, main circuit main
module main (
  input  DADOS,
  input  CLEAR,
  input  in_3,
  input  in_4,
  input  in_5,
  input  in_6,
  input  in_7,
  output out_8
);

  wire and_1_out, and_2_out, and_3_out, and_4_out, CLOCK_out, d_ff_1_q, d_ff_2_q, d_ff_3_q, d_ff_4_q;

  Clock #(.highDuration(1), .lowDuration(1)) CLOCK (.out(CLOCK_out));
  and and_1 (and_1_out, in_3, in_4);
  D_Flip_Flop #(.trigger("rising")) d_ff_1 (
    .clk(CLOCK_out), .D(DADOS), .Q(d_ff_1_q), .preset(and_1_out), .reset(CLEAR));  // open: Qn, en
  and and_2 (and_2_out, in_3, in_5);
  D_Flip_Flop #(.trigger("rising")) d_ff_2 (
    .clk(CLOCK_out), .D(d_ff_1_q), .Q(d_ff_2_q), .preset(and_2_out), .reset(CLEAR));  // open: Qn, en
  and and_3 (and_3_out, in_3, in_6);
  D_Flip_Flop #(.trigger("rising")) d_ff_3 (
    .clk(CLOCK_out), .D(d_ff_2_q), .Q(d_ff_3_q), .preset(and_3_out), .reset(CLEAR));  // open: Qn, en
  and and_4 (and_4_out, in_3, in_7);
  D_Flip_Flop #(.trigger("rising")) d_ff_4 (
    .clk(CLOCK_out), .D(d_ff_3_q), .Q(d_ff_4_q), .preset(and_4_out), .reset(CLEAR));  // open: Qn, en
  D_Flip_Flop #(.trigger("rising")) d_ff_5 (
    .clk(CLOCK_out), .D(d_ff_4_q), .Q(out_8), .reset(CLEAR));  // open: Qn, preset, en

  // Notes on the sheet:
  //   Felipe Augusto Torres
endmodule
