// Logisim project Exercicio01_guia12.circ as structural Verilog
module Exercicio01_guia12 (
  input  DADO
);

  wire CLOCK_out, j_k_ff_1_q, j_k_ff_1_qn, j_k_ff_2_q, j_k_ff_2_qn, j_k_ff_3_q, j_k_ff_3_qn, j_k_ff_4_q,
       j_k_ff_4_qn, not_1_out;

  Clock #(.highDuration(1), .lowDuration(1)) CLOCK (.out(CLOCK_out));
  not not_1 (not_1_out, DADO);
  J_K_Flip_Flop #(.trigger("rising")) j_k_ff_1 (
    .J(DADO), .clk(CLOCK_out), .K(not_1_out), .Q(j_k_ff_1_q), .Qn(j_k_ff_1_qn));  // open: preset, en, reset
  J_K_Flip_Flop #(.trigger("rising")) j_k_ff_2 (
    .J(j_k_ff_3_q), .clk(CLOCK_out), .K(j_k_ff_3_qn), .Q(j_k_ff_2_q), .Qn(j_k_ff_2_qn));  // open: preset, en, reset
  J_K_Flip_Flop #(.trigger("rising")) j_k_ff_3 (
    .J(j_k_ff_1_q), .clk(CLOCK_out), .K(j_k_ff_1_qn), .Q(j_k_ff_3_q), .Qn(j_k_ff_3_qn));  // open: preset, en, reset
  J_K_Flip_Flop #(.trigger("rising")) j_k_ff_4 (
    .J(j_k_ff_2_q), .clk(CLOCK_out), .K(j_k_ff_2_qn), .Q(j_k_ff_4_q), .Qn(j_k_ff_4_qn));  // open: preset, en, reset
  J_K_Flip_Flop #(.trigger("rising")) j_k_ff_5 (
    .J(j_k_ff_4_q), .clk(CLOCK_out), .K(j_k_ff_4_qn));  // open: Q, Qn, preset, en, reset

  // Notes on the sheet:
  //   Registrador para a direita de 5 bits
  //   Marcos Felipe Martins Silva-415719
endmodule

module Exercicio02_guia12 (
  input  DADO,
  input  in_2,
  input  in_3,
  input  in_4,
  input  in_5,
  input  in_6,
  input  in_7
);

  wire and_1_out, and_2_out, and_3_out, and_4_out, and_5_out, CLOCK_out, not_1_out, s_r_ff_1_q, s_r_ff_1_qn,
       s_r_ff_2_q, s_r_ff_2_qn, s_r_ff_3_q, s_r_ff_3_qn, s_r_ff_4_q, s_r_ff_4_qn;

  Clock #(.highDuration(1), .lowDuration(1)) CLOCK (.out(CLOCK_out));
  not not_1 (not_1_out, DADO);
  and and_1 (and_1_out, in_2, in_3);
  S_R_Flip_Flop #(.trigger("rising")) s_r_ff_1 (
    .S(DADO), .clk(CLOCK_out), .R(not_1_out), .Q(s_r_ff_1_q), .Qn(s_r_ff_1_qn), .preset(and_1_out));  // open: reset, en
  and and_2 (and_2_out, in_2, in_4);
  S_R_Flip_Flop #(.trigger("rising")) s_r_ff_2 (
    .S(s_r_ff_3_q), .clk(CLOCK_out), .R(s_r_ff_3_qn), .Q(s_r_ff_2_q), .Qn(s_r_ff_2_qn), .preset(and_3_out));  // open: reset, en
  S_R_Flip_Flop #(.trigger("rising")) s_r_ff_3 (
    .S(s_r_ff_1_q), .clk(CLOCK_out), .R(s_r_ff_1_qn), .Q(s_r_ff_3_q), .Qn(s_r_ff_3_qn), .preset(and_2_out));  // open: reset, en
  and and_3 (and_3_out, in_2, in_5);
  S_R_Flip_Flop #(.trigger("rising")) s_r_ff_4 (
    .S(s_r_ff_2_q), .clk(CLOCK_out), .R(s_r_ff_2_qn), .Q(s_r_ff_4_q), .Qn(s_r_ff_4_qn), .preset(and_4_out));  // open: reset, en
  and and_4 (and_4_out, in_2, in_6);
  S_R_Flip_Flop #(.trigger("rising")) s_r_ff_5 (
    .S(s_r_ff_4_q), .clk(CLOCK_out), .R(s_r_ff_4_qn), .preset(and_5_out));  // open: Q, Qn, reset, en
  and and_5 (and_5_out, in_2, in_7);

  // Notes on the sheet:
  //   Conversor paralelo-série com 5 bits
  //   Marcos Felipe Martins Silva-415719
endmodule

module Exercicio03_guia12 (
  input  RESET
);

  wire j_k_ff_2_q, j_k_ff_3_q, not_1_out, not_2_out, not_3_out, not_4_out, not_5_out, not_6_out, PULSO_out;

  Clock #(.highDuration(1), .lowDuration(1)) PULSO (.out(PULSO_out));
  J_K_Flip_Flop #(.trigger("rising")) j_k_ff_1 (
    .J(1'b1), .clk(not_1_out), .K(1'b1), .preset(not_2_out), .reset(RESET));  // open: Q, Qn, en
  not not_1 (not_1_out, j_k_ff_2_q);
  not not_2 (not_2_out, 1'b1);
  J_K_Flip_Flop #(.trigger("rising")) j_k_ff_2 (
    .J(1'b1), .clk(not_3_out), .K(1'b1), .Q(j_k_ff_2_q), .preset(not_4_out), .reset(RESET));  // open: Qn, en
  not not_3 (not_3_out, j_k_ff_3_q);
  not not_4 (not_4_out, 1'b1);
  not not_5 (not_5_out, PULSO_out);
  J_K_Flip_Flop #(.trigger("rising")) j_k_ff_3 (
    .J(1'b1), .clk(not_5_out), .K(1'b1), .Q(j_k_ff_3_q), .preset(not_6_out), .reset(RESET));  // open: Qn, en
  not not_6 (not_6_out, 1'b1);

  // Notes on the sheet:
  //   Contador de pulsos crescente com 3 bits
  //   Marcos Felipe Martins Silva-415719
endmodule

module Exercicio04_guia12 (
  input  DADO
);

  wire j_k_ff_2_q, j_k_ff_2_qn, j_k_ff_3_q, j_k_ff_3_qn, j_k_ff_4_q, j_k_ff_4_qn, j_k_ff_5_q, j_k_ff_5_qn,
       not_1_out, PULSO_out;

  Clock #(.highDuration(1), .lowDuration(1)) PULSO (.out(PULSO_out));
  J_K_Flip_Flop #(.trigger("rising")) j_k_ff_1 (
    .J(j_k_ff_2_q), .clk(PULSO_out), .K(j_k_ff_2_qn));  // open: Q, Qn, preset, en, reset
  J_K_Flip_Flop #(.trigger("rising")) j_k_ff_2 (
    .J(j_k_ff_3_q), .clk(PULSO_out), .K(j_k_ff_3_qn), .Q(j_k_ff_2_q), .Qn(j_k_ff_2_qn));  // open: preset, en, reset
  J_K_Flip_Flop #(.trigger("rising")) j_k_ff_3 (
    .J(j_k_ff_4_q), .clk(PULSO_out), .K(j_k_ff_4_qn), .Q(j_k_ff_3_q), .Qn(j_k_ff_3_qn));  // open: preset, en, reset
  J_K_Flip_Flop #(.trigger("rising")) j_k_ff_4 (
    .J(j_k_ff_5_q), .clk(PULSO_out), .K(j_k_ff_5_qn), .Q(j_k_ff_4_q), .Qn(j_k_ff_4_qn));  // open: preset, en, reset
  not not_1 (not_1_out, DADO);
  J_K_Flip_Flop #(.trigger("rising")) j_k_ff_5 (
    .J(DADO), .clk(PULSO_out), .K(not_1_out), .Q(j_k_ff_5_q), .Qn(j_k_ff_5_qn));  // open: preset, en, reset

  // Notes on the sheet:
  //   Registrador de deslocamento para a esquerda com 5 bits
  //   Marcos Felipe Martins Silva-415719
endmodule

module Exercicio05_guia12 (
  input  RESET
);

  wire j_k_ff_2_q, j_k_ff_3_q, not_1_out, not_2_out, not_3_out, PULSO_out;

  not not_1 (not_1_out, 1'b1);
  Clock #(.highDuration(1), .lowDuration(1)) PULSO (.out(PULSO_out));
  J_K_Flip_Flop #(.trigger("rising")) j_k_ff_1 (
    .J(1'b1), .clk(j_k_ff_2_q), .K(1'b1), .preset(not_1_out), .reset(RESET));  // open: Q, Qn, en
  not not_2 (not_2_out, 1'b1);
  J_K_Flip_Flop #(.trigger("rising")) j_k_ff_2 (
    .J(1'b1), .clk(j_k_ff_3_q), .K(1'b1), .Q(j_k_ff_2_q), .preset(not_2_out), .reset(RESET));  // open: Qn, en
  not not_3 (not_3_out, 1'b1);
  J_K_Flip_Flop #(.trigger("rising")) j_k_ff_3 (
    .J(1'b1), .clk(PULSO_out), .K(1'b1), .Q(j_k_ff_3_q), .preset(not_3_out), .reset(RESET));  // open: Qn, en

  // Notes on the sheet:
  //   Contador de pulsos decrescente com 3 bits
  //   Marcos Felipe Martins Silva-415719
endmodule
