// Logisim project 3.circ as structural Verilog: 1 circuit, main circuit main
module main (
  input  in_1,
  input  CLEAR
);

  wire clock_1_out, j_k_ff_2_q, j_k_ff_3_q, not_1_out, not_2_out;

  Clock #(.highDuration(1), .lowDuration(1)) clock_1 (.out(clock_1_out));
  not not_1 (not_1_out, j_k_ff_2_q);
  J_K_Flip_Flop #(.trigger("rising")) j_k_ff_1 (
    .J(in_1), .clk(not_1_out), .K(in_1), .reset(CLEAR));  // open: Q, Qn, preset, en
  not not_2 (not_2_out, j_k_ff_3_q);
  J_K_Flip_Flop #(.trigger("rising")) j_k_ff_2 (
    .J(in_1), .clk(not_2_out), .K(in_1), .Q(j_k_ff_2_q), .reset(CLEAR));  // open: Qn, preset, en
  J_K_Flip_Flop #(.trigger("rising")) j_k_ff_3 (
    .J(in_1), .clk(clock_1_out), .K(in_1), .Q(j_k_ff_3_q), .reset(CLEAR));  // open: Qn, preset, en

  // Notes on the sheet:
  //   Luciana Cristina Silva - 365575
endmodule
