// Logisim project circ_12.circ as structural Verilog: 3 circuits, main circuit Exercicio01
module Exercicio01 (
  input  in_1,
  input  in_2
);

  wire clock_1_out, j_k_ff_1_q, j_k_ff_1_qn, j_k_ff_2_q, j_k_ff_2_qn, j_k_ff_3_q, j_k_ff_3_qn, j_k_ff_4_q,
       j_k_ff_4_qn, not_1_out;

  Clock #(.highDuration(1), .lowDuration(1)) clock_1 (.out(clock_1_out));
  not not_1 (not_1_out, in_1);
  J_K_Flip_Flop #(.trigger("rising")) j_k_ff_1 (
    .J(in_1), .clk(clock_1_out), .K(not_1_out), .Q(j_k_ff_1_q), .Qn(j_k_ff_1_qn), .reset(in_2));  // open: preset, en
  J_K_Flip_Flop #(.trigger("rising")) j_k_ff_2 (
    .J(j_k_ff_1_q), .clk(clock_1_out), .K(j_k_ff_1_qn), .Q(j_k_ff_2_q), .Qn(j_k_ff_2_qn), .reset(in_2));  // open: preset, en
  J_K_Flip_Flop #(.trigger("rising")) j_k_ff_3 (
    .J(j_k_ff_2_q), .clk(clock_1_out), .K(j_k_ff_2_qn), .Q(j_k_ff_3_q), .Qn(j_k_ff_3_qn), .reset(in_2));  // open: preset, en
  J_K_Flip_Flop #(.trigger("rising")) j_k_ff_4 (
    .J(j_k_ff_3_q), .clk(clock_1_out), .K(j_k_ff_3_qn), .Q(j_k_ff_4_q), .Qn(j_k_ff_4_qn), .reset(in_2));  // open: preset, en
  J_K_Flip_Flop #(.trigger("rising")) j_k_ff_5 (
    .J(j_k_ff_4_q), .clk(clock_1_out), .K(j_k_ff_4_qn), .reset(in_2));  // open: Q, Qn, preset, en

  // Notes on the sheet:
  //   Igor Rodrigues de Oliveira - 380771
endmodule

module Exercicio02 (
  input  in_1,
  input  in_2,
  input  in_3,
  input  in_4,
  input  in_5,
  input  in_6,
  input  in_7,
  input  in_8
);

  wire and_1_out, and_2_out, and_3_out, and_4_out, and_5_out, clock_1_out, not_1_out, s_r_ff_1_q,
       s_r_ff_1_qn, s_r_ff_2_q, s_r_ff_2_qn, s_r_ff_3_q, s_r_ff_3_qn, s_r_ff_4_q, s_r_ff_4_qn;

  Clock #(.highDuration(1), .lowDuration(1)) clock_1 (.out(clock_1_out));
  S_R_Flip_Flop #(.trigger("rising")) s_r_ff_1 (
    .S(in_1), .clk(clock_1_out), .R(not_1_out), .Q(s_r_ff_1_q), .Qn(s_r_ff_1_qn), .preset(and_1_out),
    .reset(in_2));  // open: en
  not not_1 (not_1_out, in_1);
  and and_1 (and_1_out, in_8, in_3);
  S_R_Flip_Flop #(.trigger("rising")) s_r_ff_2 (
    .S(s_r_ff_1_q), .clk(clock_1_out), .R(s_r_ff_1_qn), .Q(s_r_ff_2_q), .Qn(s_r_ff_2_qn), .preset(and_2_out),
    .reset(in_2));  // open: en
  and and_2 (and_2_out, in_8, in_4);
  S_R_Flip_Flop #(.trigger("rising")) s_r_ff_3 (
    .S(s_r_ff_2_q), .clk(clock_1_out), .R(s_r_ff_2_qn), .Q(s_r_ff_3_q), .Qn(s_r_ff_3_qn), .preset(and_3_out),
    .reset(in_2));  // open: en
  and and_3 (and_3_out, in_8, in_5);
  S_R_Flip_Flop #(.trigger("rising")) s_r_ff_4 (
    .S(s_r_ff_3_q), .clk(clock_1_out), .R(s_r_ff_3_qn), .Q(s_r_ff_4_q), .Qn(s_r_ff_4_qn), .preset(and_4_out),
    .reset(in_2));  // open: en
  and and_4 (and_4_out, in_8, in_6);
  and and_5 (and_5_out, in_8, in_7);
  S_R_Flip_Flop #(.trigger("rising")) s_r_ff_5 (
    .S(s_r_ff_4_q), .clk(clock_1_out), .R(s_r_ff_4_qn), .preset(and_5_out), .reset(in_2));  // open: Q, Qn, en

  // Notes on the sheet:
  //   Igor Rodrigues de Oliveira - 380771
endmodule

module Exercicio03 (
  input  in_1
);

  wire clock_1_out, j_k_ff_2_q, j_k_ff_3_q, j_k_ff_3_qn, not_1_out, not_2_out, not_3_out, not_4_out,
       not_5_out, not_6_out;

  not not_1 (not_1_out, j_k_ff_2_q);
  Clock #(.highDuration(1), .lowDuration(1)) clock_1 (.out(clock_1_out));
  not not_2 (not_2_out, 1'b1);
  J_K_Flip_Flop #(.trigger("rising")) j_k_ff_1 (
    .J(1'b1), .clk(not_1_out), .K(1'b1), .preset(not_2_out), .reset(in_1));  // open: Q, Qn, en
  not not_3 (not_3_out, j_k_ff_3_q);
  not not_4 (not_4_out, 1'b1);
  J_K_Flip_Flop #(.trigger("rising")) j_k_ff_2 (
    .J(1'b1), .clk(not_3_out), .K(1'b1), .Q(j_k_ff_2_q), .preset(not_4_out), .reset(in_1));  // open: Qn, en
  not not_5 (not_5_out, clock_1_out);
  not not_6 (not_6_out, 1'b1);
  J_K_Flip_Flop #(.trigger("rising")) j_k_ff_3 (
    .J(1'b1), .clk(not_5_out), .K(1'b1), .Q(j_k_ff_3_q), .Qn(j_k_ff_3_qn), .preset(not_6_out), .reset(in_1));  // open: en

  // Notes on the sheet:
  //   Igor Rodrigues de Oliveira - 380771
endmodule
