// Logisim project contadordepulsos_crescente.circ as structural Verilog: 1 circuit, main circuit contadordepusos_crescente.circ
module contadordepusos_crescente_circ (
  input  entrada,
  input  reset,
  output out_3
);

  wire clock_1_out, j_k_ff_2_q, j_k_ff_3_q;

  Clock #(.highDuration(1), .lowDuration(1)) clock_1 (.out(clock_1_out));
  J_K_Flip_Flop #(.trigger("rising")) j_k_ff_1 (
    .J(entrada), .clk(j_k_ff_2_q), .K(entrada), .Q(out_3), .en(reset));  // open: Qn, preset, reset
  J_K_Flip_Flop #(.trigger("rising")) j_k_ff_2 (
    .J(entrada), .clk(j_k_ff_3_q), .K(entrada), .Q(j_k_ff_2_q), .en(reset));  // open: Qn, preset, reset
  J_K_Flip_Flop #(.trigger("rising")) j_k_ff_3 (
    .J(entrada), .clk(clock_1_out), .K(entrada), .Q(j_k_ff_3_q), .en(reset));  // open: Qn, preset, reset

  // Notes on the sheet:
  //   clok
  //   contador de pusos crescente de 3 bits
  //   esse circuito tem uma unica entrada
  //   ele ira alternar os bits internos ao jk
  //   a
  //   iniciando em zero e reset em zero nao acontece nada
  //   mas se iniciar com 1 e ocilar com o clock e colocar reset em 1
  //   b
  //   É DECRESCENTE
  //   CLOCK+RESET+ENTRADA=1)para toggle
  //   c
  //   Nome :Eneas
  //   Numero : 376507
endmodule
