// Logisim project conversor_paralelo_serie.circ as structural Verilog
module conversor_paralelo_serie_circ (
  input  load,
  input  e,
  input  d,
  input  c,
  input  b,
  input  a,
  input  clier,
  output a_2
);

  wire and_1_out, and_2_out, and_3_out, and_4_out, and_5_out, clock_1_out, s_r_ff_1_q, s_r_ff_2_q,
       s_r_ff_3_q, s_r_ff_4_q, s_r_ff_5_qn;

  Clock #(.highDuration(1), .lowDuration(1)) clock_1 (.out(clock_1_out));
  and and_1 (and_1_out, e, load);
  S_R_Flip_Flop #(.trigger("rising")) s_r_ff_1 (
    .clk(clock_1_out), .R(s_r_ff_5_qn), .Q(s_r_ff_1_q), .preset(and_1_out), .en(clier));  // open: S, Qn, reset
  S_R_Flip_Flop #(.trigger("rising")) s_r_ff_2 (
    .S(s_r_ff_1_q), .clk(clock_1_out), .R(s_r_ff_5_qn), .Q(s_r_ff_2_q), .preset(and_2_out), .en(clier));  // open: Qn, reset
  and and_2 (and_2_out, d, load);
  and and_3 (and_3_out, c, load);
  S_R_Flip_Flop #(.trigger("rising")) s_r_ff_3 (
    .S(s_r_ff_2_q), .clk(clock_1_out), .R(s_r_ff_5_qn), .Q(s_r_ff_3_q), .preset(and_3_out), .en(clier));  // open: Qn, reset
  and and_4 (and_4_out, b, load);
  S_R_Flip_Flop #(.trigger("rising")) s_r_ff_4 (
    .S(s_r_ff_3_q), .clk(clock_1_out), .R(clier), .Q(s_r_ff_4_q), .preset(and_4_out), .en(clier));  // open: Qn, reset
  and and_5 (and_5_out, a, load);
  S_R_Flip_Flop #(.trigger("rising")) s_r_ff_5 (
    .S(s_r_ff_4_q), .clk(clock_1_out), .R(clier), .Q(a_2), .Qn(s_r_ff_5_qn), .preset(and_5_out), .en(clier));  // open: reset

  // Notes on the sheet:
  //   clok
  //   e
  //   se colocar o load em 1 ele guarda o resultado
  //   somente se as entradas forem igual a 1
  //   conversor paralelo-serie com 5 bits
  //   d
  //   c
  //   b
  //   Nome: Eneas
  //   matricula:376507
endmodule
