// Logisim project registrador_de_deslocamentodireita.circ as structural Verilog: 1 circuit, main circuit registrador_de_deslocamentodireita.circ
module registrador_de_deslocamentodireita_circ (
  input  dados,
  input  clier,
  output se,
  output sd,
  output sc,
  output sb,
  output sa
);

  wire clock_1_out, j_k_ff_1_qn, j_k_ff_2_qn, j_k_ff_3_qn, j_k_ff_4_qn;

  Clock #(.highDuration(1), .lowDuration(1)) clock_1 (.out(clock_1_out));
  not not_1 (clock_1_out, dados);
  J_K_Flip_Flop #(.trigger("rising")) j_k_ff_1 (
    .J(dados), .clk(clock_1_out), .K(clock_1_out), .Q(se), .Qn(j_k_ff_1_qn), .en(clier));  // open: preset, reset
  J_K_Flip_Flop #(.trigger("rising")) j_k_ff_2 (
    .J(se), .clk(clock_1_out), .K(j_k_ff_1_qn), .Q(sd), .Qn(j_k_ff_2_qn), .en(clier));  // open: preset, reset
  J_K_Flip_Flop #(.trigger("rising")) j_k_ff_3 (
    .J(sd), .clk(clock_1_out), .K(j_k_ff_2_qn), .Q(sc), .Qn(j_k_ff_3_qn), .en(clier));  // open: preset, reset
  J_K_Flip_Flop #(.trigger("rising")) j_k_ff_4 (
    .J(sc), .clk(clock_1_out), .K(j_k_ff_3_qn), .Q(sb), .Qn(j_k_ff_4_qn), .en(clier));  // open: preset, reset
  J_K_Flip_Flop #(.trigger("rising")) j_k_ff_5 (
    .J(sb), .clk(clock_1_out), .K(j_k_ff_4_qn), .Q(sa), .en(clier));  // open: Qn, preset, reset

  // Notes on the sheet:
  //   clok
  //   TEM UMA LINHA EXTRA ENTRE K E O CLOCK
  //   01111
  //   0111
  //   011
  //   01
  //   0
  //   circuito registrador de deslocamento para direita
  //   e
  //   d
  //   d
  //   e
  //   1
  //   1
  //   1
  //   1
  //   1
  //   1
  //   0
  //   0
  //   b
  //   c
  //   1
  //   1
  //   1
  //   1
  //   1
  //   1
  //   0
  //   0
  //   Nome: Eneas 
  //   c
  //   a
  //   1
  //   1
  //   11
  //   1
  //   111
  //   1
  //   0
  //   1111
  //   01111
  //   Nome:376507
  //   b
  //   ele tera esses valores na saida
  //   a
endmodule
