// Logisim project guia12_ex01.circ as structural Verilog: 1 circuit, main circuit main
module main (
  input  data,
  input  clear,
  output out_3,
  output out_4,
  output out_5,
  output out_6,
  output out_7
);

  wire clock_1_out;

  Clock #(.highDuration(1), .lowDuration(1)) clock_1 (.out(clock_1_out));
  D_Flip_Flop #(.trigger("rising")) d_ff_1 (
    .clk(clock_1_out), .D(data), .Q(out_3), .reset(clear));  // open: Qn, preset, en
  D_Flip_Flop #(.trigger("rising")) d_ff_2 (
    .clk(clock_1_out), .D(out_3), .Q(out_4), .reset(clear));  // open: Qn, preset, en
  D_Flip_Flop #(.trigger("rising")) d_ff_3 (
    .clk(clock_1_out), .D(out_4), .Q(out_5), .reset(clear));  // open: Qn, preset, en
  D_Flip_Flop #(.trigger("rising")) d_ff_4 (
    .clk(clock_1_out), .D(out_5), .Q(out_6), .reset(clear));  // open: Qn, preset, en
  D_Flip_Flop #(.trigger("rising")) d_ff_5 (
    .clk(clock_1_out), .D(out_6), .Q(out_7), .reset(clear));  // open: Qn, preset, en
endmodule
