// Logisim project guia12_ex02.circ as structural Verilog: 1 circuit, main circuit main
module main (
  input  clear,
  input  load,
  input  in_3,
  input  in_4,
  input  in_5,
  input  in_6,
  input  in_7,
  output out_8,
  output out_9,
  output out_10,
  output out_11,
  output out_12
);

  wire and_1_out, and_2_out, and_3_out, and_4_out, and_5_out, clock_1_out;

  Clock #(.highDuration(1), .lowDuration(1)) clock_1 (.out(clock_1_out));
  and and_1 (and_1_out, load, in_3);
  D_Flip_Flop #(.trigger("rising")) d_ff_1 (
    .clk(clock_1_out), .D(1'b0), .Q(out_8), .preset(and_1_out), .reset(clear));  // open: Qn, en
  and and_2 (and_2_out, load, in_3);
  D_Flip_Flop #(.trigger("rising")) d_ff_2 (
    .clk(clock_1_out), .D(out_8), .Q(out_9), .preset(and_2_out), .reset(clear));  // open: Qn, en
  and and_3 (and_3_out, load, in_3);
  D_Flip_Flop #(.trigger("rising")) d_ff_3 (
    .clk(clock_1_out), .D(out_9), .Q(out_10), .preset(and_3_out), .reset(clear));  // open: Qn, en
  and and_4 (and_4_out, load, in_3);
  D_Flip_Flop #(.trigger("rising")) d_ff_4 (
    .clk(clock_1_out), .D(out_10), .Q(out_11), .preset(and_4_out), .reset(clear));  // open: Qn, en
  and and_5 (and_5_out, load, in_3);
  D_Flip_Flop #(.trigger("rising")) d_ff_5 (
    .clk(clock_1_out), .D(out_11), .Q(out_12), .preset(and_5_out), .reset(clear));  // open: Qn, en

  assign in_4 = in_3;
  assign in_5 = in_3;
  assign in_6 = in_3;
  assign in_7 = in_3;
endmodule
