// Logisim project guia12_ex03.circ as structural Verilog: 1 circuit, main circuit main
module main (
  input  clear,
  output out_2,
  output out_3,
  output out_4
);

  wire clock_1_out, j_k_ff_2_q, j_k_ff_3_q;

  Clock #(.highDuration(1), .lowDuration(1)) clock_1 (.out(clock_1_out));
  J_K_Flip_Flop #(.trigger("rising")) j_k_ff_1 (
    .J(1'b1), .clk(j_k_ff_2_q), .K(1'b1), .Qn(out_2), .reset(clear));  // open: Q, preset, en
  J_K_Flip_Flop #(.trigger("rising")) j_k_ff_2 (
    .J(1'b1), .clk(j_k_ff_3_q), .Q(j_k_ff_2_q), .Qn(out_3), .reset(clear));  // open: K, preset, en
  J_K_Flip_Flop #(.trigger("rising")) j_k_ff_3 (
    .J(1'b1), .clk(clock_1_out), .K(1'b1), .Q(j_k_ff_3_q), .Qn(out_4), .reset(clear));  // open: preset, en
endmodule
