// Logisim project guia12_ex05.circ as structural Verilog: 1 circuit, main circuit main
module main (
  input  clear,
  output out_2,
  output out_3,
  output out_4
);

  wire clock_1_out;

  Clock #(.highDuration(1), .lowDuration(1)) clock_1 (.out(clock_1_out));
  J_K_Flip_Flop #(.trigger("rising")) j_k_ff_1 (
    .J(1'b1), .clk(out_3), .K(1'b1), .Qn(out_2), .reset(clear));  // open: Q, preset, en
  J_K_Flip_Flop #(.trigger("rising")) j_k_ff_2 (
    .J(1'b1), .clk(out_4), .K(1'b1), .Qn(out_3), .reset(clear));  // open: Q, preset, en
  J_K_Flip_Flop #(.trigger("rising")) j_k_ff_3 (
    .J(1'b1), .clk(clock_1_out), .K(1'b1), .Qn(out_4), .reset(clear));  // open: Q, preset, en
endmodule
