// Logisim project Circuitos.circ as structural Verilog: 5 circuits, main circuit Deslocamento para a direita com 5 bits
module Deslocamento_para_a_direita_com_5_bits (
  input  DATA,
  input  CLEAR,
  output out_3,
  output out_4,
  output out_5,
  output out_6,
  output out_7
);

  wire CLK_out;

  Clock #(.highDuration(1), .lowDuration(1)) CLK (.out(CLK_out));
  D_Flip_Flop #(.trigger("rising")) d_ff_1 (.clk(CLK_out), .D(DATA), .Q(out_3), .reset(CLEAR));  // open: Qn, preset, en
  D_Flip_Flop #(.trigger("rising")) d_ff_2 (
    .clk(CLK_out), .D(out_3), .Q(out_4), .reset(CLEAR));  // open: Qn, preset, en
  D_Flip_Flop #(.trigger("rising")) d_ff_3 (
    .clk(CLK_out), .D(out_4), .Q(out_5), .reset(CLEAR));  // open: Qn, preset, en
  D_Flip_Flop #(.trigger("rising")) d_ff_4 (
    .clk(CLK_out), .D(out_5), .Q(out_6), .reset(CLEAR));  // open: Qn, preset, en
  D_Flip_Flop #(.trigger("rising")) d_ff_5 (
    .clk(CLK_out), .D(out_6), .Q(out_7), .reset(CLEAR));  // open: Qn, preset, en

  // Notes on the sheet:
  //   Nádia de Souza Maciel Vieira Ferreira
endmodule

module Conversor_paralelo_em_serie_5_bits (
  input  CLEAR,
  input  LOAD,
  input  D4,
  input  D3,
  input  D2,
  input  D1,
  input  D0,
  output out_8,
  output out_9,
  output out_10,
  output out_11,
  output out_12
);

  wire and_1_out, and_2_out, and_3_out, and_4_out, and_5_out, CLOCK_out;

  Clock #(.highDuration(1), .lowDuration(1)) CLOCK (.out(CLOCK_out));
  D_Flip_Flop #(.trigger("rising")) d_ff_1 (
    .clk(CLOCK_out), .D(1'b0), .Q(out_8), .preset(and_1_out), .reset(CLEAR));  // open: Qn, en
  and and_1 (and_1_out, LOAD, D4);
  D_Flip_Flop #(.trigger("rising")) d_ff_2 (
    .clk(CLOCK_out), .D(out_8), .Q(out_9), .preset(and_2_out), .reset(CLEAR));  // open: Qn, en
  and and_2 (and_2_out, LOAD, D3);
  D_Flip_Flop #(.trigger("rising")) d_ff_3 (
    .clk(CLOCK_out), .D(out_9), .Q(out_10), .preset(and_3_out), .reset(CLEAR));  // open: Qn, en
  and and_3 (and_3_out, LOAD, D2);
  D_Flip_Flop #(.trigger("rising")) d_ff_4 (
    .clk(CLOCK_out), .D(out_10), .Q(out_11), .preset(and_4_out), .reset(CLEAR));  // open: Qn, en
  and and_4 (and_4_out, LOAD, D1);
  D_Flip_Flop #(.trigger("rising")) d_ff_5 (
    .clk(CLOCK_out), .D(out_11), .Q(out_12), .preset(and_5_out), .reset(CLEAR));  // open: Qn, en
  and and_5 (and_5_out, LOAD, D0);

  // Notes on the sheet:
  //   412737 - Fabricio Rodrigues de Souza
endmodule

module Contador_Crescente_de_3_bits (
  input  X1,
  input  PULSE,
  input  CLEAR,
  output out_4,
  output out_5,
  output out_6
);

  wire j_k_ff_2_q, j_k_ff_3_q;

  J_K_Flip_Flop #(.trigger("rising")) j_k_ff_1 (
    .J(X1), .clk(j_k_ff_2_q), .K(X1), .Qn(out_4), .reset(CLEAR));  // open: Q, preset, en
  J_K_Flip_Flop #(.trigger("rising")) j_k_ff_2 (
    .J(X1), .clk(j_k_ff_3_q), .K(X1), .Q(j_k_ff_2_q), .Qn(out_5), .reset(CLEAR));  // open: preset, en
  J_K_Flip_Flop #(.trigger("rising")) j_k_ff_3 (
    .J(X1), .clk(PULSE), .K(X1), .Q(j_k_ff_3_q), .Qn(out_6), .reset(CLEAR));  // open: preset, en

  // Notes on the sheet:
  //   412737 - Fabricio Rodrigues de Souza
endmodule

module Deslocamento_para_a_esquerda_com_5_bits (
  input  DATA,
  input  CLEAR,
  output out_3,
  output out_4,
  output out_5,
  output out_6,
  output out_7
);

  wire CLK_out;

  Clock #(.highDuration(1), .lowDuration(1)) CLK (.out(CLK_out));
  D_Flip_Flop #(.trigger("rising")) d_ff_1 (
    .clk(CLK_out), .D(out_4), .Q(out_3), .reset(CLEAR));  // open: Qn, preset, en
  D_Flip_Flop #(.trigger("rising")) d_ff_2 (
    .clk(CLK_out), .D(out_5), .Q(out_4), .reset(CLEAR));  // open: Qn, preset, en
  D_Flip_Flop #(.trigger("rising")) d_ff_3 (
    .clk(CLK_out), .D(out_6), .Q(out_5), .reset(CLEAR));  // open: Qn, preset, en
  D_Flip_Flop #(.trigger("rising")) d_ff_4 (
    .clk(CLK_out), .D(out_7), .Q(out_6), .reset(CLEAR));  // open: Qn, preset, en
  D_Flip_Flop #(.trigger("rising")) d_ff_5 (.clk(CLK_out), .D(DATA), .Q(out_7), .reset(CLEAR));  // open: Qn, preset, en

  // Notes on the sheet:
  //   412737 - Fabricio Rodrigues de Souza
endmodule

module Contador_de_pulsos_decrescente_3_bits (
  input  X1,
  input  PULSE,
  input  CLEAR,
  output out_4,
  output out_5,
  output out_6
);

  J_K_Flip_Flop #(.trigger("rising")) j_k_ff_1 (
    .J(X1), .clk(out_5), .K(X1), .Qn(out_4), .reset(CLEAR));  // open: Q, preset, en
  J_K_Flip_Flop #(.trigger("rising")) j_k_ff_2 (
    .J(X1), .clk(out_6), .K(X1), .Qn(out_5), .reset(CLEAR));  // open: Q, preset, en
  J_K_Flip_Flop #(.trigger("rising")) j_k_ff_3 (
    .J(X1), .clk(PULSE), .K(X1), .Qn(out_6), .reset(CLEAR));  // open: Q, preset, en

  // Notes on the sheet:
  //   412737 - Fabricio Rodrigues de Souza
endmodule
