// Logisim project Guia_13.circ as structural Verilog
module Registrador (
  input  [1:0] dado,
  input  clk,
  output [1:0] saida
);

  D_Flip_Flop #(.trigger("rising")) d_ff_1 (.clk(clk), .D(dado[1]), .Q(saida[1]));  // open: Qn, preset, en, reset
  D_Flip_Flop #(.trigger("rising")) d_ff_2 (.clk(clk), .D(dado[0]), .Q(saida[0]));  // open: Qn, preset, en, reset

  // Notes on the sheet:
  //   Registrador
  //   Celso R Franca Jr
endmodule

module Lu (
  input  [1:0] dado_1,
  input  [1:0] dado_2,
  output [1:0] not__b,
  output [1:0] not__a,
  output [1:0] \and ,
  output [1:0] \or ,
  output [1:0] \xor 
);

  wire clock_1_out;
  wire [1:0] registrador_1_saida, registrador_2_saida;

  Registrador registrador_1 (.dado(dado_1), .clk(clock_1_out), .saida(registrador_1_saida));
  Clock #(.highDuration(1), .lowDuration(1)) clock_1 (.out(clock_1_out));
  Registrador registrador_2 (.dado(dado_2), .clk(clock_1_out), .saida(registrador_2_saida));
  assign not__b = ~registrador_2_saida;  // NOT_Gate not_1, 2 bits wide
  assign not__a = ~registrador_1_saida;  // NOT_Gate not_2, 2 bits wide
  assign \and  = registrador_2_saida & registrador_1_saida;  // AND_Gate and_1, 2 bits wide
  assign \or  = registrador_2_saida | registrador_1_saida;  // OR_Gate or_1, 2 bits wide
  assign \xor  = registrador_2_saida ^ registrador_1_saida;  // XOR_Gate xor_1, 2 bits wide

  // Notes on the sheet:
  //   registrador b
  //   Unidade Lógica
  //   registrador a
  //   Celso R Franca Jr
endmodule

module Lu___2 (
  input  [1:0] dado_1,
  input  [1:0] dado_2,
  output [1:0] \nand ,
  output [1:0] \nor ,
  output [1:0] \xnor 
);

  wire clock_1_out;
  wire [1:0] registrador_1_saida, registrador_2_saida;

  Clock #(.highDuration(1), .lowDuration(1)) clock_1 (.out(clock_1_out));
  Registrador registrador_1 (.dado(dado_1), .clk(clock_1_out), .saida(registrador_1_saida));
  Registrador registrador_2 (.dado(dado_2), .clk(clock_1_out), .saida(registrador_2_saida));
  assign \nand  = ~(registrador_2_saida & registrador_1_saida);  // NAND_Gate nand_1, 2 bits wide
  assign \nor  = ~(registrador_2_saida | registrador_1_saida);  // NOR_Gate nor_1, 2 bits wide
  assign \xnor  = ~(registrador_2_saida ^ registrador_1_saida);  // XNOR_Gate xnor_1, 2 bits wide

  // Notes on the sheet:
  //   registrador b
  //   Unidade Lógica
  //   registrador a
  //   Celso R Franca Jr
endmodule

module Lu___3 (
  input  [1:0] dado_1,
  input  [1:0] dado_2,
  output dado2_e_prime_maior_que_dado1,
  output dado2_e_prime_igual_ao_dado1,
  output dado2_e_prime_menor_que_dado1
);

  wire clock_1_out;
  wire [1:0] registrador_1_saida, registrador_2_saida;

  Clock #(.highDuration(1), .lowDuration(1)) clock_1 (.out(clock_1_out));
  Registrador registrador_1 (.dado(dado_1), .clk(clock_1_out), .saida(registrador_1_saida));
  Registrador registrador_2 (.dado(dado_2), .clk(clock_1_out), .saida(registrador_2_saida));
  comparador comparador_1 (
    .dado1(registrador_1_saida), .dado_2(registrador_2_saida), .maior(dado2_e_prime_maior_que_dado1),
    .igual(dado2_e_prime_igual_ao_dado1), .menor(dado2_e_prime_menor_que_dado1));

  // Notes on the sheet:
  //   registrador b
  //   Unidade Lógica
  //   registrador a
  //   Comparador
  //   em relação ao dado 2
  //   Celso R Franca Jr
endmodule

module Registrador_4bits (
  input  [3:0] dado,
  input  clk,
  output [3:0] saida
);

  D_Flip_Flop #(.trigger("rising")) d_ff_1 (.clk(clk), .D(dado[3]), .Q(saida[3]));  // open: Qn, preset, en, reset
  D_Flip_Flop #(.trigger("rising")) d_ff_2 (.clk(clk), .D(dado[2]), .Q(saida[2]));  // open: Qn, preset, en, reset
  D_Flip_Flop #(.trigger("rising")) d_ff_3 (.clk(clk), .D(dado[1]), .Q(saida[1]));  // open: Qn, preset, en, reset
  D_Flip_Flop #(.trigger("rising")) d_ff_4 (.clk(clk), .D(dado[0]), .Q(saida[0]));  // open: Qn, preset, en, reset

  // Notes on the sheet:
  //   Registrador
  //   Celso R franca Jr
endmodule

module Lu___4 (
  input  [3:0] dado_1,
  input  [3:0] dado_2,
  output [3:0] not1,
  output [3:0] not2,
  output [3:0] \nand ,
  output [3:0] \nor ,
  output [3:0] nxor,
  output [3:0] \and ,
  output [3:0] \or ,
  output [3:0] \xor 
);

  wire clock_1_out;
  wire [3:0] registrador_4bits_1_saida, registrador_4bits_2_saida;

  Clock #(.highDuration(1), .lowDuration(1)) clock_1 (.out(clock_1_out));
  Registrador_4bits registrador_4bits_1 (.dado(dado_1), .clk(clock_1_out), .saida(registrador_4bits_1_saida));
  Registrador_4bits registrador_4bits_2 (.dado(dado_2), .clk(clock_1_out), .saida(registrador_4bits_2_saida));
  assign not1 = ~registrador_4bits_1_saida;  // NOT_Gate not_1, 4 bits wide
  assign not2 = ~registrador_4bits_2_saida;  // NOT_Gate not_2, 4 bits wide
  assign \nand  = ~(registrador_4bits_2_saida & registrador_4bits_1_saida);  // NAND_Gate nand_1, 4 bits wide
  assign \nor  = ~(registrador_4bits_2_saida | registrador_4bits_1_saida);  // NOR_Gate nor_1, 4 bits wide
  assign nxor = ~(registrador_4bits_2_saida ^ registrador_4bits_1_saida);  // XNOR_Gate xnor_1, 4 bits wide
  assign \and  = registrador_4bits_2_saida & registrador_4bits_1_saida;  // AND_Gate and_1, 4 bits wide
  assign \or  = registrador_4bits_2_saida | registrador_4bits_1_saida;  // OR_Gate or_1, 4 bits wide
  assign \xor  = registrador_4bits_2_saida ^ registrador_4bits_1_saida;  // XOR_Gate xor_1, 4 bits wide

  // Notes on the sheet:
  //   registrador b
  //   Unidade Lógica
  //   registrador a
  //   Celso R Franca Jr
endmodule

module igual (
  input  [1:0] dado_1,
  input  [1:0] dado_2,
  output _1___iguais
);

  wire xnor_1_out, xnor_2_out;

  xnor xnor_1 (xnor_1_out, dado_2[1], dado_1[1]);
  xnor xnor_2 (xnor_2_out, dado_2[0], dado_1[0]);
  and and_1 (_1___iguais, xnor_1_out, xnor_2_out);

  // Notes on the sheet:
  //   Testa se sao iguais
  //   2 - diferentes
  //   Celso R Franca Jr
endmodule

module maior (
  input  [1:0] dado_1,
  input  [1:0] dado_2,
  output out_3
);

  wire and_1_out, and_2_out, and_3_out;
  wire [1:0] not_1_out;

  assign not_1_out = ~dado_2;  // NOT_Gate not_1, 2 bits wide
  and and_1 (and_1_out, dado_1[1], not_1_out[1]);
  and and_2 (and_2_out, dado_1[1], not_1_out[0], dado_1[0]);
  and and_3 (and_3_out, dado_1[0], not_1_out[1], not_1_out[0]);
  or or_1 (out_3, and_1_out, and_2_out, and_3_out);

  // Notes on the sheet:
  //   Maior
  //   Celso R Franca Jr
endmodule

module menor (
  input  [1:0] dado_1,
  input  [1:0] dado_2,
  output out_3
);

  wire and_1_out, and_2_out, and_3_out;
  wire [1:0] not_1_out;

  assign not_1_out = ~dado_1;  // NOT_Gate not_1, 2 bits wide
  and and_1 (and_1_out, not_1_out[1], dado_2[1]);
  and and_2 (and_2_out, not_1_out[1], dado_2[0], not_1_out[0]);
  and and_3 (and_3_out, not_1_out[0], dado_2[1], dado_2[0]);
  or or_1 (out_3, and_1_out, and_2_out, and_3_out);

  // Notes on the sheet:
  //   Menor
  //   Celso R Franca Jr
endmodule

module comparador (
  input  [1:0] dado1,
  input  [1:0] dado_2,
  output maior,
  output igual,
  output menor
);

  maior maior_1 (.dado_1(dado_2), .dado_2(dado1), .out_3(maior));
  igual igual_1 (.dado_1(dado_2), .dado_2(dado1), ._1___iguais(igual));
  menor menor_1 (.dado_1(dado_2), .dado_2(dado1), .out_3(menor));

  // Notes on the sheet:
  //   Comparador
  //   Celso R Franca Jr
endmodule
