// Logisim project LU_2bits.circ as structural Verilog: 10 circuits, main circuit LU_2bits
module LU_2bits (
  input  [1:0] A,
  input  [3:0] Enable_Load_A1_A0,
  input  [1:0] B,
  input  [3:0] Enable_Load_B3_B2_B1_B0,
  input  [3:0] Chave,
  output [1:0] out_6
);

  wire clk_out;
  wire [0:0] comparador_2bits_1_out_3, comparador_2bits_1_out_4, comparador_2bits_1_out_5;
  wire [1:0] and_2bits_1_s, nand_2bits_1_s, nor_2bits_1_s, not_2bits_1_x_prime, not_2bits_2_x_prime,
       or_2bits_1_s, registrador_2bits_1_out_4, registrador_2bits_2_out_4, xnor_2bits_1_s, xor_2bits_1_s;

  Clock #(.highDuration(1), .lowDuration(1)) clk (.out(clk_out));
  registrador_2bits registrador_2bits_1 (
    .CLK(clk_out), .Variavel(A), .Data(Enable_Load_A1_A0), .out_4(registrador_2bits_1_out_4));
  registrador_2bits registrador_2bits_2 (
    .CLK(clk_out), .Variavel(B), .Data(Enable_Load_B3_B2_B1_B0), .out_4(registrador_2bits_2_out_4));
  not_2bits not_2bits_1 (.x(registrador_2bits_1_out_4), .x_prime(not_2bits_1_x_prime));
  not_2bits not_2bits_2 (.x(registrador_2bits_2_out_4), .x_prime(not_2bits_2_x_prime));
  and_2bits and_2bits_1 (.a(registrador_2bits_1_out_4), .b(registrador_2bits_2_out_4), .s(and_2bits_1_s));
  or_2bits or_2bits_1 (.a(registrador_2bits_1_out_4), .b(registrador_2bits_2_out_4), .s(or_2bits_1_s));
  xor_2bits xor_2bits_1 (.a(registrador_2bits_1_out_4), .b(registrador_2bits_2_out_4), .s(xor_2bits_1_s));
  nand_2bits nand_2bits_1 (.a(registrador_2bits_1_out_4), .b(registrador_2bits_2_out_4), .s(nand_2bits_1_s));
  nor_2bits nor_2bits_1 (.a(registrador_2bits_1_out_4), .b(registrador_2bits_2_out_4), .s(nor_2bits_1_s));
  xnor_2bits xnor_2bits_1 (.a(registrador_2bits_1_out_4), .b(registrador_2bits_2_out_4), .s(xnor_2bits_1_s));
  comparador_2bits comparador_2bits_1 (
    .a(registrador_2bits_1_out_4), .b(registrador_2bits_2_out_4), .out_3(comparador_2bits_1_out_3[0]),
    .out_4(comparador_2bits_1_out_4[0]), .out_5(comparador_2bits_1_out_5[0]));
  Multiplexer #(.select(4), .width(2)) multiplexer_1 (
    .in0(not_2bits_1_x_prime), .in1(not_2bits_2_x_prime), .in2(and_2bits_1_s), .in3(or_2bits_1_s),
    .in4(xor_2bits_1_s), .in5(nand_2bits_1_s), .in6(nor_2bits_1_s), .in7(xnor_2bits_1_s),
    .in8({1'b0, comparador_2bits_1_out_3[0]}), .in9({1'b0, comparador_2bits_1_out_4[0]}),
    .in10({1'b0, comparador_2bits_1_out_5[0]}), .out(out_6), .sel(Chave));  // open: in11, in12, in13, in14, in15

  // Notes on the sheet:
  //   Márcia Cibele Martins Carneiro - 404591
  //   Márcia Cibele Martins Carneiro - 404591
  //   Operações lógicas para 4bits em cada entrada.
  //   NOTA
  //   NOTB
  //   AND
  //   OR
  //   XOR
  //   NAND
  //   NOR
  //   XNOR
  //   <,=,>
endmodule

module registrador_2bits (
  input  CLK,
  input  [1:0] Variavel,
  input  [3:0] Data,
  output [1:0] out_4
);

  wire d_ff_1_q, d_ff_2_q;

  D_Flip_Flop #(.trigger("rising")) d_ff_1 (
    .clk(CLK), .D(Variavel[0]), .Q(d_ff_1_q), .en(Data[0]));  // open: Qn, preset, reset
  D_Flip_Flop #(.trigger("rising")) d_ff_2 (
    .clk(CLK), .D(Variavel[1]), .Q(d_ff_2_q), .en(Data[2]));  // open: Qn, preset, reset
  assign out_4[0] = Data[1] ? d_ff_1_q : 1'bz;  // Controlled_Buffer controlled_buffer_1
  assign out_4[1] = Data[3] ? d_ff_2_q : 1'bz;  // Controlled_Buffer controlled_buffer_2

  // Notes on the sheet:
  //   Márcia Cibele Martins Carneiro - 404591
  //   Márcia Cibele Martins Carneiro - 404591
  //    Registrador de 2 bits
endmodule

module not_2bits (
  input  [1:0] x,
  output [1:0] x_prime
);

  assign x_prime = ~x;  // NOT_Gate not_1, 2 bits wide

  // Notes on the sheet:
  //   Márcia Cibele Martins Carneiro - 404591
  //   Márcia Cibele Martins Carneiro - 404591
  //   NOT de 2 bits
endmodule

module and_2bits (
  input  [1:0] a,
  input  [1:0] b,
  output [1:0] s
);

  assign s = a & b;  // AND_Gate and_1, 2 bits wide

  // Notes on the sheet:
  //   Márcia Cibele Martins Carneiro - 404591
  //   Márcia Cibele Martins Carneiro - 404591
  //   AND de 2 bits
endmodule

module xor_2bits (
  input  [1:0] a,
  input  [1:0] b,
  output [1:0] s
);

  assign s = a ^ b;  // XOR_Gate xor_1, 2 bits wide

  // Notes on the sheet:
  //   Márcia Cibele Martins Carneiro - 404591
  //   Márcia Cibele Martins Carneiro - 404591
  //   XOR de 2 bits
endmodule

module or_2bits (
  input  [1:0] a,
  input  [1:0] b,
  output [1:0] s
);

  assign s = a | b;  // OR_Gate or_1, 2 bits wide

  // Notes on the sheet:
  //   Márcia Cibele Martins Carneiro - 404591
  //   Márcia Cibele Martins Carneiro - 404591
  //   OR de 4 bits
endmodule

module nand_2bits (
  input  [1:0] a,
  input  [1:0] b,
  output [1:0] s
);

  assign s = ~(a & b);  // NAND_Gate nand_1, 2 bits wide

  // Notes on the sheet:
  //   Márcia Cibele Martins Carneiro - 404591
  //   Márcia Cibele Martins Carneiro - 404591
  //   NAND de 2 bits
endmodule

module xnor_2bits (
  input  [1:0] a,
  input  [1:0] b,
  output [1:0] s
);

  assign s = ~(a ^ b);  // XNOR_Gate xnor_1, 2 bits wide

  // Notes on the sheet:
  //   Márcia Cibele Martins Carneiro - 404591
  //   Márcia Cibele Martins Carneiro - 404591
  //   XNOR de 4 bits
endmodule

module nor_2bits (
  input  [1:0] a,
  input  [1:0] b,
  output [1:0] s
);

  assign s = ~(a | b);  // NOR_Gate nor_1, 2 bits wide

  // Notes on the sheet:
  //   Márcia Cibele Martins Carneiro - 404591
  //   Márcia Cibele Martins Carneiro - 404591
  //   NOR de 2 bits
endmodule

module comparador_2bits (
  input  [1:0] a,
  input  [1:0] b,
  output out_3,
  output out_4,
  output out_5
);

  Comparator #(.width(2), .mode("twosComplement")) comparator_1 (.a(a), .b(b), .gt(out_3), .eq(out_4), .lt(out_5));

  // Notes on the sheet:
  //   Márcia Cibele Martins Carneiro - 404591
  //   Márcia Cibele Martins Carneiro - 404591
  //   Comparador de 2 bits
endmodule
