// Logisim project LU_4bits.circ as structural Verilog: 10 circuits, main circuit LU_4bits
module LU_4bits (
  input  [3:0] A,
  input  [7:0] Enable_Load_A3_A2_A1_A0,
  input  [3:0] B,
  input  [7:0] Enable_Load_B3_B2_B1_B0,
  input  [3:0] Chave,
  output [3:0] out_6
);

  wire clk_out;
  wire [0:0] undriven, undriven_2, undriven_3;
  wire [3:0] and_4bits_1_s, nand_4bits_1_s, nor_4bits_1_s, not_4bits_1_x_prime, not_4bits_2_x_prime,
       or_4bits_1_s, registrador_4bits_1_out_4, registrador_4bits_2_out_4, xnor_4bits_1_s, xor_4bits_1_s;

  Clock #(.highDuration(1), .lowDuration(1)) clk (.out(clk_out));
  registrador_4bits registrador_4bits_1 (
    .CLK(clk_out), .in_2(A), .in_3(Enable_Load_A3_A2_A1_A0), .out_4(registrador_4bits_1_out_4));
  registrador_4bits registrador_4bits_2 (
    .CLK(clk_out), .in_2(B), .in_3(Enable_Load_B3_B2_B1_B0), .out_4(registrador_4bits_2_out_4));
  not_4bits not_4bits_1 (.x(registrador_4bits_1_out_4), .x_prime(not_4bits_1_x_prime));
  not_4bits not_4bits_2 (.x(registrador_4bits_2_out_4), .x_prime(not_4bits_2_x_prime));
  and_4bits and_4bits_1 (.a(registrador_4bits_1_out_4), .b(registrador_4bits_2_out_4), .s(and_4bits_1_s));
  or_4bits or_4bits_1 (.a(registrador_4bits_1_out_4), .b(registrador_4bits_2_out_4), .s(or_4bits_1_s));
  xor_4bits xor_4bits_1 (.a(registrador_4bits_1_out_4), .b(registrador_4bits_2_out_4), .s(xor_4bits_1_s));
  nand_4bits nand_4bits_1 (.a(registrador_4bits_1_out_4), .b(registrador_4bits_2_out_4), .s(nand_4bits_1_s));
  nor_4bits nor_4bits_1 (.a(registrador_4bits_1_out_4), .b(registrador_4bits_2_out_4), .s(nor_4bits_1_s));
  xnor_4bits xnor_4bits_1 (.a(registrador_4bits_1_out_4), .b(registrador_4bits_2_out_4), .s(xnor_4bits_1_s));
  comparador_4bits comparador_4bits_1 (
    .a(registrador_4bits_1_out_4), .b(registrador_4bits_2_out_4));  // open: out_3, out_4, out_5
  Multiplexer #(.select(4), .width(4)) multiplexer_1 (
    .in0(not_4bits_1_x_prime), .in1(not_4bits_2_x_prime), .in2(and_4bits_1_s), .in3(or_4bits_1_s),
    .in4(xor_4bits_1_s), .in5(nand_4bits_1_s), .in6(nor_4bits_1_s), .in7(xnor_4bits_1_s),
    .in8({3'b000, undriven[0]}), .in9({3'b000, undriven_2[0]}), .in10({3'b000, undriven_3[0]}), .out(out_6),
    .sel(Chave));  // open: in11, in12, in13, in14, in15

  // Notes on the sheet:
  //   Márcia Cibele Martins Carneiro - 404591
  //   Márcia Cibele Martins Carneiro - 404591
  //   Operações lógicas para 4bits em cada entrada.
  //   NOTA
  //   NOTB
  //   AND
  //   OR
  //   XOR
  //   NAND
  //   NOR
  //   XNOR
  //   <,=,>
endmodule

module registrador_4bits (
  input  CLK,
  input  [3:0] in_2,
  input  [7:0] in_3,
  output [3:0] out_4
);

  wire d_ff_1_q, d_ff_2_q, d_ff_3_q, d_ff_4_q;

  D_Flip_Flop #(.trigger("rising")) d_ff_1 (
    .clk(CLK), .D(in_2[3]), .Q(d_ff_1_q), .en(in_3[7]));  // open: Qn, preset, reset
  D_Flip_Flop #(.trigger("rising")) d_ff_2 (
    .clk(CLK), .D(in_2[1]), .Q(d_ff_2_q), .en(in_3[5]));  // open: Qn, preset, reset
  D_Flip_Flop #(.trigger("rising")) d_ff_3 (
    .clk(CLK), .D(in_2[2]), .Q(d_ff_3_q), .en(in_3[3]));  // open: Qn, preset, reset
  D_Flip_Flop #(.trigger("rising")) d_ff_4 (
    .clk(CLK), .D(in_2[0]), .Q(d_ff_4_q), .en(in_3[1]));  // open: Qn, preset, reset
  assign out_4[3] = in_3[6] ? d_ff_1_q : 1'bz;  // Controlled_Buffer controlled_buffer_1
  assign out_4[1] = in_3[4] ? d_ff_2_q : 1'bz;  // Controlled_Buffer controlled_buffer_2
  assign out_4[2] = in_3[2] ? d_ff_3_q : 1'bz;  // Controlled_Buffer controlled_buffer_3
  assign out_4[0] = in_3[0] ? d_ff_4_q : 1'bz;  // Controlled_Buffer controlled_buffer_4

  // Notes on the sheet:
  //   Márcia Cibele Martins Carneiro - 404591
  //   Márcia Cibele Martins Carneiro - 404591
  //    Registrador de 4 bits
endmodule

module not_4bits (
  input  [3:0] x,
  output [3:0] x_prime
);

  assign x_prime = ~x;  // NOT_Gate not_1, 4 bits wide

  // Notes on the sheet:
  //   Márcia Cibele Martins Carneiro - 404591
  //   Márcia Cibele Martins Carneiro - 404591
  //   NOT de 4 bits
endmodule

module and_4bits (
  input  [3:0] a,
  input  [3:0] b,
  output [3:0] s
);

  assign s = a & b;  // AND_Gate and_1, 4 bits wide

  // Notes on the sheet:
  //   Márcia Cibele Martins Carneiro - 404591
  //   Márcia Cibele Martins Carneiro - 404591
  //   AND de 4 bits
endmodule

module xor_4bits (
  input  [3:0] a,
  input  [3:0] b,
  output [3:0] s
);

  assign s = a ^ b;  // XOR_Gate xor_1, 4 bits wide

  // Notes on the sheet:
  //   Márcia Cibele Martins Carneiro - 404591
  //   Márcia Cibele Martins Carneiro - 404591
  //   XOR de 4 bits
endmodule

module or_4bits (
  input  [3:0] a,
  input  [3:0] b,
  output [3:0] s
);

  assign s = a | b;  // OR_Gate or_1, 4 bits wide

  // Notes on the sheet:
  //   Márcia Cibele Martins Carneiro - 404591
  //   Márcia Cibele Martins Carneiro - 404591
  //   OR de 4 bits
endmodule

module nand_4bits (
  input  [3:0] a,
  input  [3:0] b,
  output [3:0] s
);

  assign s = ~(a & b);  // NAND_Gate nand_1, 4 bits wide

  // Notes on the sheet:
  //   Márcia Cibele Martins Carneiro - 404591
  //   Márcia Cibele Martins Carneiro - 404591
  //   NAND de 4 bits
endmodule

module xnor_4bits (
  input  [3:0] a,
  input  [3:0] b,
  output [3:0] s
);

  assign s = ~(a ^ b);  // XNOR_Gate xnor_1, 4 bits wide

  // Notes on the sheet:
  //   Márcia Cibele Martins Carneiro - 404591
  //   Márcia Cibele Martins Carneiro - 404591
  //   XNOR de 4 bits
endmodule

module nor_4bits (
  input  [3:0] a,
  input  [3:0] b,
  output [3:0] s
);

  assign s = ~(a | b);  // NOR_Gate nor_1, 4 bits wide

  // Notes on the sheet:
  //   Márcia Cibele Martins Carneiro - 404591
  //   Márcia Cibele Martins Carneiro - 404591
  //   NOR de 4 bits
endmodule

module comparador_4bits (
  input  [3:0] a,
  input  [3:0] b,
  output out_3,
  output out_4,
  output out_5
);

  Comparator #(.width(4), .mode("twosComplement")) comparator_1 (.a(a), .b(b), .gt(out_3), .eq(out_4), .lt(out_5));

  // Notes on the sheet:
  //   Márcia Cibele Martins Carneiro - 404591
  //   Márcia Cibele Martins Carneiro - 404591
  //   Comparador de 4 bits
endmodule
