// Logisim project G13E1.circ as structural Verilog: 2 circuits, main circuit main
module main (
  input  [1:0] _1,
  input  [1:0] _2,
  output [1:0] Not__1,
  output [1:0] Not__2,
  output [1:0] _1_AND__2,
  output [1:0] _1_OR__2,
  output [1:0] _1_XOR__2
);

  wire CLK_out;
  wire [1:0] reg_s_1_out_3, reg_s_2_out_3;

  Clock #(.highDuration(1), .lowDuration(1)) CLK (.out(CLK_out));
  reg_s reg_s_1 (.in_1(_1), .in_2(CLK_out), .out_3(reg_s_1_out_3));
  reg_s reg_s_2 (.in_1(_2), .in_2(CLK_out), .out_3(reg_s_2_out_3));
  assign Not__1 = ~reg_s_1_out_3;  // NOT_Gate not_1, 2 bits wide
  assign Not__2 = ~reg_s_2_out_3;  // NOT_Gate not_2, 2 bits wide
  assign _1_AND__2 = reg_s_1_out_3 & reg_s_2_out_3;  // AND_Gate and_1, 2 bits wide
  assign _1_OR__2 = reg_s_1_out_3 | reg_s_2_out_3;  // OR_Gate or_1, 2 bits wide
  assign _1_XOR__2 = reg_s_1_out_3 ^ reg_s_2_out_3;  // XOR_Gate xor_1, 2 bits wide

  // Notes on the sheet:
  //   Matrícula:405782
  //   Guia 13_01 -  LU 2 bits - Not, And, Or, Xor
  //   Nome: Alan Diniz Nogueira Machado
endmodule

module reg_s (
  input  [1:0] in_1,
  input  in_2,
  output [1:0] out_3
);

  D_Flip_Flop #(.trigger("rising")) d_ff_1 (.clk(in_2), .D(in_1[1]), .Q(out_3[1]));  // open: Qn, preset, en, reset
  D_Flip_Flop #(.trigger("rising")) d_ff_2 (.clk(in_2), .D(in_1[0]), .Q(out_3[0]));  // open: Qn, preset, en, reset
endmodule
