// Logisim project G13E3.circ as structural Verilog: 5 circuits, main circuit main
module main (
  input  [1:0] _1,
  input  [1:0] _2,
  output out_3,
  output out_4,
  output out_5
);

  wire CLK_out;
  wire [1:0] reg_s_1_out_3, reg_s_2_out_3;

  Clock #(.highDuration(1), .lowDuration(1)) CLK (.out(CLK_out));
  reg_s reg_s_1 (.in_1(_1), .in_2(CLK_out), .out_3(reg_s_1_out_3));
  reg_s reg_s_2 (.in_1(_2), .in_2(CLK_out), .out_3(reg_s_2_out_3));
  equal equal_1 (.in_1(reg_s_1_out_3), .in_2(reg_s_2_out_3), .out_3(out_3));
  menor menor_1 (.in_1(reg_s_1_out_3), .in_2(reg_s_2_out_3), .out_3(out_4));
  maior maior_1 (.in_1(reg_s_1_out_3), .in_2(reg_s_2_out_3), .out_3(out_5));

  // Notes on the sheet:
  //   Matrícula:405782
  //   Guia 13_03 -  LU 2 bits - Maior, Menor, Igual
  //   Nome: Alan Diniz Nogueira Machado
endmodule

module equal (
  input  [1:0] in_1,
  input  [1:0] in_2,
  output out_3
);

  wire xnor_1_out, xnor_2_out;

  xnor xnor_1 (xnor_1_out, in_1[1], in_2[1]);
  and and_1 (out_3, xnor_1_out, xnor_2_out);
  xnor xnor_2 (xnor_2_out, in_2[0], in_1[0]);
endmodule

module maior (
  input  [1:0] in_1,
  input  [1:0] in_2,
  output out_3
);

  wire and_1_out, and_2_out, and_3_out;
  wire [1:0] not_1_out;

  assign not_1_out = ~in_2;  // NOT_Gate not_1, 2 bits wide
  and and_1 (and_1_out, in_1[1], not_1_out[1]);
  and and_2 (and_2_out, in_1[1], in_1[0], not_1_out[0]);
  and and_3 (and_3_out, in_1[0], not_1_out[0], not_1_out[1]);
  or or_1 (out_3, and_1_out, and_2_out, and_3_out);
endmodule

module menor (
  input  [1:0] in_1,
  input  [1:0] in_2,
  output out_3
);

  wire and_1_out, and_2_out, and_3_out;
  wire [1:0] not_1_out;

  assign not_1_out = ~in_1;  // NOT_Gate not_1, 2 bits wide
  and and_1 (and_1_out, not_1_out[1], in_2[1]);
  and and_2 (and_2_out, not_1_out[1], not_1_out[0], in_2[0]);
  and and_3 (and_3_out, not_1_out[0], in_2[0], in_2[1]);
  or or_1 (out_3, and_1_out, and_2_out, and_3_out);
endmodule

module reg_s (
  input  [1:0] in_1,
  input  in_2,
  output [1:0] out_3
);

  D_Flip_Flop #(.trigger("rising")) d_ff_1 (.clk(in_2), .D(in_1[1]), .Q(out_3[1]));  // open: Qn, preset, en, reset
  D_Flip_Flop #(.trigger("rising")) d_ff_2 (.clk(in_2), .D(in_1[0]), .Q(out_3[0]));  // open: Qn, preset, en, reset
endmodule
