// Logisim project Guia13.circ as structural Verilog: 9 circuits, main circuit main
module main (
  input  [1:0] in_1,
  input  [1:0] in_2,
  input  in_3,
  input  in_4,
  input  Enable,
  input  Clear,
  input  [3:0] A,
  input  [3:0] B,
  input  [2:0] Chave,
  output [1:0] And_out,
  output [1:0] Or_Out,
  output [1:0] Xor_Out,
  output [1:0] Not_Out,
  output [1:0] Nand_Out,
  output [1:0] Nor_Out,
  output [1:0] Xnor_Out,
  output A___B_Out,
  output A___B_Out_2,
  output A___B_Out_3,
  output [3:0] Out
);

  wire clock_2_out, Clock_out;
  wire [3:0] exercicio04_1_out_6, exercicio04_1_out_7, exercicio04_1_out_8, exercicio04_1_out_9,
       exercicio04_1_out_10, exercicio04_1_out_11, exercicio04_1_out_12;

  Exercicio03 exercicio03_1 (
    .A(in_1), .B(in_2), .Enable(in_3), .Clear_2(in_4), .Clock(clock_2_out), .And_Out(And_out),
    .Or_Out(Or_Out), .Xor_Out(Xor_Out), .Not_Out(Not_Out), .Nand_Out(Nand_Out), .Nor_Out(Nor_Out),
    .Xnor_Out(Xnor_Out), .A___B_Out(A___B_Out), .A___B_Out_2(A___B_Out_2), .A___B_Out_3(A___B_Out_3));  // open: Clear, A_Out, B_Out, Enable_Out, Clear_Out, Clock_Out
  Clock #(.highDuration(1), .lowDuration(1)) Clock (.out(Clock_out));
  Exercicio04 exercicio04_1 (
    .in_4(A), .in_5(B), .in_1(Enable), .in_2(Clear), .in_3(Clock_out), .out_6(exercicio04_1_out_6),
    .out_7(exercicio04_1_out_7), .out_8(exercicio04_1_out_8), .out_9(exercicio04_1_out_9),
    .out_10(exercicio04_1_out_10), .out_11(exercicio04_1_out_11), .out_12(exercicio04_1_out_12));  // open: out_13, out_14, out_15, out_16, out_17
  Clock #(.highDuration(1), .lowDuration(1)) clock_2 (.out(clock_2_out));
  Multiplexer #(.select(3), .width(4)) multiplexer_1 (
    .in0(exercicio04_1_out_6), .in1(exercicio04_1_out_7), .in2(exercicio04_1_out_8),
    .in3(exercicio04_1_out_9), .in4(exercicio04_1_out_10), .in5(exercicio04_1_out_11),
    .in6(exercicio04_1_out_12), .out(Out), .sel(Chave));  // open: in7

  // Notes on the sheet:
  //   Bruno Santiago Pinheiro - 405792
endmodule

module Exercicio01 (
  input  [1:0] A,
  input  [1:0] B,
  input  Enable,
  input  Clear,
  input  Clock,
  output [1:0] And_Out,
  output [1:0] Or_Out,
  output [1:0] Xor_Out,
  output [1:0] Not_Out,
  output [1:0] A_out,
  output [1:0] B_out,
  output Enable_out,
  output Clear_out,
  output Clock_out
);

  wire and_1_out, and_2_out, or_1_out, or_2_out, xor_1_out, xor_2_out;

  and and_1 (and_1_out, A[0], B[0]);
  and and_2 (and_2_out, B[1], A[1]);
  or or_1 (or_1_out, A[0], B[0]);
  or or_2 (or_2_out, A[1], B[1]);
  xor xor_1 (xor_1_out, A[0], B[0]);
  xor xor_2 (xor_2_out, A[1], B[1]);
  D_Flip_Flop #(.trigger("rising")) d_ff_1 (
    .clk(Clock), .D(and_1_out), .Q(And_Out[0]), .en(Enable), .reset(Clear));  // open: Qn, preset
  D_Flip_Flop #(.trigger("rising")) d_ff_2 (
    .clk(Clock), .D(and_2_out), .Q(And_Out[1]), .en(Enable), .reset(Clear));  // open: Qn, preset
  D_Flip_Flop #(.trigger("rising")) d_ff_3 (
    .clk(Clock), .D(or_1_out), .Q(Or_Out[0]), .en(Enable), .reset(Clear));  // open: Qn, preset
  D_Flip_Flop #(.trigger("rising")) d_ff_4 (
    .clk(Clock), .D(or_2_out), .Q(Or_Out[1]), .en(Enable), .reset(Clear));  // open: Qn, preset
  D_Flip_Flop #(.trigger("rising")) d_ff_5 (
    .clk(Clock), .D(xor_1_out), .Q(Xor_Out[0]), .en(Enable), .reset(Clear));  // open: Qn, preset
  D_Flip_Flop #(.trigger("rising")) d_ff_6 (
    .clk(Clock), .D(xor_2_out), .Q(Xor_Out[1]), .en(Enable), .reset(Clear));  // open: Qn, preset
  D_Flip_Flop #(.trigger("rising")) d_ff_7 (
    .clk(Clock), .D(A[0]), .Qn(Not_Out[0]), .en(Enable), .reset(Clear));  // open: Q, preset
  D_Flip_Flop #(.trigger("rising")) d_ff_8 (
    .clk(Clock), .D(A[1]), .Qn(Not_Out[1]), .en(Enable), .reset(Clear));  // open: Q, preset

  assign A_out = A;
  assign B_out = B;
  assign Clear_out = Clear;
  assign Clock_out = Clock;
  assign Enable_out = Enable;

  // Notes on the sheet:
  //   Bruno Santiago Pinheiro - 405792
endmodule

module Exercicio02 (
  input  [1:0] A,
  input  [1:0] B,
  input  Enable,
  input  Clear,
  input  Clock,
  output [1:0] And_Out,
  output [1:0] Or_Out,
  output [1:0] Xor_Out,
  output [1:0] Not_Out,
  output [1:0] Nand_Out,
  output [1:0] Nor_Out,
  output [1:0] Xnor_Out,
  output [1:0] A_Out,
  output [1:0] B_Out,
  output Enable_2,
  output Clear_2,
  output Clock_2
);

  wire nand_1_out, nand_2_out, nor_1_out, nor_2_out, xnor_1_out, xnor_2_out;

  Exercicio01 exercicio01_1 (
    .A(A), .B(B), .Enable(Enable), .Clear(Clear), .Clock(Clock), .A_out(A_Out), .B_out(B_Out),
    .Enable_out(Enable_2), .Clear_out(Clear_2), .Clock_out(Clock_2), .And_Out(And_Out), .Or_Out(Or_Out),
    .Xor_Out(Xor_Out), .Not_Out(Not_Out));
  nand nand_1 (nand_1_out, A_Out[0], B_Out[0]);
  nand nand_2 (nand_2_out, A_Out[1], B_Out[1]);
  nor nor_1 (nor_1_out, A_Out[0], B_Out[0]);
  nor nor_2 (nor_2_out, A_Out[1], B_Out[1]);
  xnor xnor_1 (xnor_1_out, A_Out[0], B_Out[0]);
  xnor xnor_2 (xnor_2_out, A_Out[1], B_Out[1]);
  D_Flip_Flop #(.trigger("rising")) d_ff_1 (
    .clk(Clock_2), .D(nand_1_out), .Q(Nand_Out[0]), .en(Enable_2), .reset(Clear_2));  // open: Qn, preset
  D_Flip_Flop #(.trigger("rising")) d_ff_2 (
    .clk(Clock_2), .D(nand_2_out), .Q(Nand_Out[1]), .en(Enable_2), .reset(Clear_2));  // open: Qn, preset
  D_Flip_Flop #(.trigger("rising")) d_ff_3 (
    .clk(Clock_2), .D(nor_1_out), .Q(Nor_Out[0]), .en(Enable_2), .reset(Clear_2));  // open: Qn, preset
  D_Flip_Flop #(.trigger("rising")) d_ff_4 (
    .clk(Clock_2), .D(nor_2_out), .Q(Nor_Out[1]), .en(Enable_2), .reset(Clear_2));  // open: Qn, preset
  D_Flip_Flop #(.trigger("rising")) d_ff_5 (
    .clk(Clock_2), .D(xnor_1_out), .Q(Xnor_Out[0]), .en(Enable_2), .reset(Clear_2));  // open: Qn, preset
  D_Flip_Flop #(.trigger("rising")) d_ff_6 (
    .clk(Clock_2), .D(xnor_2_out), .Q(Xnor_Out[1]), .en(Enable_2), .reset(Clear_2));  // open: Qn, preset
endmodule

module Exercicio03 (
  input  Clear,
  input  [1:0] A,
  input  [1:0] B,
  input  Enable,
  input  Clear_2,
  input  Clock,
  output [1:0] And_Out,
  output [1:0] Or_Out,
  output [1:0] Xor_Out,
  output [1:0] Not_Out,
  output [1:0] Nand_Out,
  output [1:0] Nor_Out,
  output [1:0] Xnor_Out,
  output A___B_Out,
  output A___B_Out_2,
  output A___B_Out_3,
  output [1:0] A_Out,
  output [1:0] B_Out,
  output Enable_Out,
  output Clear_Out,
  output Clock_Out
);

  wire igual_1_out_3, maior_1_out_3, menor_1_out_3;

  Exercicio02 exercicio02_1 (
    .A(A), .B(B), .Enable(Enable), .Clear(Clear_2), .Clock(Clock), .A_Out(A_Out), .B_Out(B_Out),
    .Enable_2(Enable_Out), .Clear_2(Clear_Out), .Clock_2(Clock_Out), .And_Out(And_Out), .Or_Out(Or_Out),
    .Xor_Out(Xor_Out), .Not_Out(Not_Out), .Nand_Out(Nand_Out), .Nor_Out(Nor_Out), .Xnor_Out(Xnor_Out));
  Maior maior_1 (.A(A_Out), .B(B_Out), .out_3(maior_1_out_3));
  Menor menor_1 (.A(A_Out), .B(B_Out), .out_3(menor_1_out_3));
  Igual igual_1 (.in_1(A_Out), .in_2(B_Out), .out_3(igual_1_out_3));
  D_Flip_Flop #(.trigger("rising")) d_ff_1 (
    .clk(Clock_Out), .D(maior_1_out_3), .Q(A___B_Out), .en(Enable_Out), .reset(Clear_Out));  // open: Qn, preset
  D_Flip_Flop #(.trigger("rising")) d_ff_2 (
    .clk(Clock_Out), .D(menor_1_out_3), .Q(A___B_Out_2), .en(Enable_Out), .reset(Clear_Out));  // open: Qn, preset
  D_Flip_Flop #(.trigger("rising")) d_ff_3 (
    .clk(Clock_Out), .D(igual_1_out_3), .Q(A___B_Out_3), .en(Enable_Out), .reset(Clear_Out));  // open: Qn, preset
endmodule

module Maior (
  input  [1:0] A,
  input  [1:0] B,
  output out_3
);

  wire and_1_out, and_2_out, and_3_out, not_1_out, not_2_out, not_3_out, not_4_out;

  and and_1 (and_1_out, A[1], not_1_out);
  not not_1 (not_1_out, B[1]);
  and and_2 (and_2_out, A[0], not_2_out, not_3_out);
  not not_2 (not_2_out, B[0]);
  not not_3 (not_3_out, B[1]);
  and and_3 (and_3_out, A[1], A[0], not_4_out);
  not not_4 (not_4_out, B[0]);
  or or_1 (out_3, and_1_out, and_2_out, and_3_out);
endmodule

module Menor (
  input  [1:0] A,
  input  [1:0] B,
  output out_3
);

  wire and_1_out, and_2_out, and_3_out, not_1_out, not_2_out, not_3_out, not_4_out;

  and and_1 (and_1_out, not_1_out, B[1]);
  not not_1 (not_1_out, A[1]);
  not not_2 (not_2_out, A[0]);
  and and_2 (and_2_out, not_2_out, B[0], B[1]);
  not not_3 (not_3_out, A[1]);
  not not_4 (not_4_out, A[0]);
  and and_3 (and_3_out, not_3_out, not_4_out, B[0]);
  or or_1 (out_3, and_1_out, and_2_out, and_3_out);
endmodule

module Igual (
  input  [1:0] in_1,
  input  [1:0] in_2,
  output out_3
);

  wire xor_1_out, xor_2_out;

  xor xor_1 (xor_1_out, in_1[0], in_2[0]);
  xor xor_2 (xor_2_out, in_1[1], in_2[1]);
  nor nor_1 (out_3, xor_1_out, xor_2_out);
endmodule

module Exercicio04 (
  input  in_1,
  input  in_2,
  input  in_3,
  input  [3:0] in_4,
  input  [3:0] in_5,
  output [3:0] out_6,
  output [3:0] out_7,
  output [3:0] out_8,
  output [3:0] out_9,
  output [3:0] out_10,
  output [3:0] out_11,
  output [3:0] out_12,
  output [3:0] out_13,
  output [3:0] out_14,
  output out_15,
  output out_16,
  output out_17
);

  wire [3:0] and_1_out, nand_1_out, nor_1_out, or_1_out, xnor_1_out, xor_1_out;

  assign and_1_out = in_4 & in_5;  // AND_Gate and_1, 4 bits wide
  assign or_1_out = in_4 | in_5;  // OR_Gate or_1, 4 bits wide
  assign xor_1_out = in_4 ^ in_5;  // XOR_Gate xor_1, 4 bits wide
  assign nand_1_out = ~(in_4 & in_5);  // NAND_Gate nand_1, 4 bits wide
  assign nor_1_out = ~(in_4 | in_5);  // NOR_Gate nor_1, 4 bits wide
  assign xnor_1_out = ~(in_4 ^ in_5);  // XNOR_Gate xnor_1, 4 bits wide
  D_Flip_Flop #(.trigger("rising")) d_ff_1 (
    .clk(in_2), .D(and_1_out[0]), .Q(out_6[0]), .en(in_1), .reset(in_2));  // open: Qn, preset
  D_Flip_Flop #(.trigger("rising")) d_ff_2 (
    .clk(in_2), .D(and_1_out[1]), .Q(out_6[1]), .en(in_1), .reset(in_2));  // open: Qn, preset
  D_Flip_Flop #(.trigger("rising")) d_ff_3 (
    .clk(in_2), .D(and_1_out[2]), .Q(out_6[2]), .en(in_1), .reset(in_2));  // open: Qn, preset
  D_Flip_Flop #(.trigger("rising")) d_ff_4 (
    .clk(in_2), .D(and_1_out[3]), .Q(out_6[3]), .en(in_1), .reset(in_2));  // open: Qn, preset
  D_Flip_Flop #(.trigger("rising")) d_ff_5 (
    .clk(in_2), .D(or_1_out[0]), .Q(out_7[0]), .en(in_1), .reset(in_2));  // open: Qn, preset
  D_Flip_Flop #(.trigger("rising")) d_ff_6 (
    .clk(in_2), .D(or_1_out[1]), .Q(out_7[1]), .en(in_1), .reset(in_2));  // open: Qn, preset
  D_Flip_Flop #(.trigger("rising")) d_ff_7 (
    .clk(in_2), .D(or_1_out[2]), .Q(out_7[2]), .en(in_1), .reset(in_2));  // open: Qn, preset
  D_Flip_Flop #(.trigger("rising")) d_ff_8 (
    .clk(in_2), .D(or_1_out[3]), .Q(out_7[3]), .en(in_1), .reset(in_2));  // open: Qn, preset
  D_Flip_Flop #(.trigger("rising")) d_ff_9 (
    .clk(in_2), .D(xor_1_out[0]), .Q(out_8[0]), .en(in_1), .reset(in_2));  // open: Qn, preset
  D_Flip_Flop #(.trigger("rising")) d_ff_10 (
    .clk(in_2), .D(xor_1_out[1]), .Q(out_8[1]), .en(in_1), .reset(in_2));  // open: Qn, preset
  D_Flip_Flop #(.trigger("rising")) d_ff_11 (
    .clk(in_2), .D(xor_1_out[2]), .Q(out_8[2]), .en(in_1), .reset(in_2));  // open: Qn, preset
  D_Flip_Flop #(.trigger("rising")) d_ff_12 (
    .clk(in_2), .D(xor_1_out[3]), .Q(out_8[3]), .en(in_1), .reset(in_2));  // open: Qn, preset
  D_Flip_Flop #(.trigger("rising")) d_ff_13 (
    .clk(in_2), .D(in_4[0]), .Qn(out_9[0]), .en(in_1), .reset(in_2));  // open: Q, preset
  D_Flip_Flop #(.trigger("rising")) d_ff_14 (
    .clk(in_2), .D(in_4[1]), .Qn(out_9[1]), .en(in_1), .reset(in_2));  // open: Q, preset
  D_Flip_Flop #(.trigger("rising")) d_ff_15 (
    .clk(in_2), .D(in_4[2]), .Qn(out_9[2]), .en(in_1), .reset(in_2));  // open: Q, preset
  D_Flip_Flop #(.trigger("rising")) d_ff_16 (
    .clk(in_2), .D(in_4[3]), .Qn(out_9[3]), .en(in_1), .reset(in_2));  // open: Q, preset
  D_Flip_Flop #(.trigger("rising")) d_ff_17 (
    .clk(in_2), .D(nand_1_out[0]), .Q(out_10[0]), .en(in_1), .reset(in_2));  // open: Qn, preset
  D_Flip_Flop #(.trigger("rising")) d_ff_18 (
    .clk(in_2), .D(nand_1_out[1]), .Q(out_10[1]), .en(in_1), .reset(in_2));  // open: Qn, preset
  D_Flip_Flop #(.trigger("rising")) d_ff_19 (
    .clk(in_2), .D(nand_1_out[2]), .Q(out_10[2]), .en(in_1), .reset(in_2));  // open: Qn, preset
  D_Flip_Flop #(.trigger("rising")) d_ff_20 (
    .clk(in_2), .D(nand_1_out[3]), .Q(out_10[3]), .en(in_1), .reset(in_2));  // open: Qn, preset
  D_Flip_Flop #(.trigger("rising")) d_ff_21 (
    .clk(in_2), .D(nor_1_out[0]), .Q(out_11[0]), .en(in_1), .reset(in_2));  // open: Qn, preset
  D_Flip_Flop #(.trigger("rising")) d_ff_22 (
    .clk(in_2), .D(nor_1_out[1]), .Q(out_11[1]), .en(in_1), .reset(in_2));  // open: Qn, preset
  D_Flip_Flop #(.trigger("rising")) d_ff_23 (
    .clk(in_2), .D(nor_1_out[2]), .Q(out_11[2]), .en(in_1), .reset(in_2));  // open: Qn, preset
  D_Flip_Flop #(.trigger("rising")) d_ff_24 (
    .clk(in_2), .D(nor_1_out[3]), .Q(out_11[3]), .en(in_1), .reset(in_2));  // open: Qn, preset
  D_Flip_Flop #(.trigger("rising")) d_ff_25 (
    .clk(in_2), .D(xnor_1_out[0]), .Q(out_12[0]), .en(in_1), .reset(in_2));  // open: Qn, preset
  D_Flip_Flop #(.trigger("rising")) d_ff_26 (
    .clk(in_2), .D(xnor_1_out[1]), .Q(out_12[1]), .en(in_1), .reset(in_2));  // open: Qn, preset
  D_Flip_Flop #(.trigger("rising")) d_ff_27 (
    .clk(in_2), .D(xnor_1_out[2]), .Q(out_12[2]), .en(in_1), .reset(in_2));  // open: Qn, preset
  D_Flip_Flop #(.trigger("rising")) d_ff_28 (
    .clk(in_2), .D(xnor_1_out[3]), .Q(out_12[3]), .en(in_1), .reset(in_2));  // open: Qn, preset

  assign in_3 = in_2;
  assign out_13 = in_4;
  assign out_14 = in_5;
  assign out_15 = in_1;
  assign out_16 = in_2;
  assign out_17 = in_2;
endmodule

module Igual_4Bits (
  input  [3:0] in_1,
  input  [3:0] in_2,
  output out_3
);

  wire xor_1_out, xor_2_out, xor_3_out, xor_4_out;

  xor xor_1 (xor_1_out, in_1[0], in_2[0]);
  xor xor_2 (xor_2_out, in_1[1], in_2[1]);
  xor xor_3 (xor_3_out, in_1[2], in_2[2]);
  xor xor_4 (xor_4_out, in_1[3], in_2[3]);
  nor nor_1 (out_3, xor_1_out, xor_2_out, xor_3_out, xor_4_out);
endmodule
