// Logisim project 405795_Daniel Sathler Silva.circ as structural Verilog: 10 circuits, main circuit LU_4bits
module LU_4bits (
  input  [3:0] A,
  input  [3:0] B,
  input  [3:0] Enabled,
  output [3:0] \and ,
  output [3:0] \or ,
  output [3:0] \not ,
  output [3:0] \xor ,
  output [3:0] \nand ,
  output [3:0] \nor ,
  output [3:0] \xnor ,
  output maior,
  output igual,
  output menor
);

  wire Clock_out;
  wire [3:0] registrador_4bits_1_output, registrador_4bits_2_output;

  Clock #(.highDuration(1), .lowDuration(1)) Clock (.out(Clock_out));
  registrador_4bits registrador_4bits_1 (
    .Clock(Clock_out), .Input(A), .Enabled(Enabled), .Output(registrador_4bits_1_output));
  registrador_4bits registrador_4bits_2 (
    .Clock(Clock_out), .Input(B), .Enabled(Enabled), .Output(registrador_4bits_2_output));
  and_4bits and_4bits_1 (.\input (registrador_4bits_1_output), .input_2(registrador_4bits_2_output), .\output (\and ));
  or_4bits or_4bits_1 (.\input (registrador_4bits_1_output), .input_2(registrador_4bits_2_output), .\output (\or ));
  not_4bits not_4bits_1 (.\input (registrador_4bits_1_output), .\output (\not ));
  xor_4bits xor_4bits_1 (.\input (registrador_4bits_1_output), .input_2(registrador_4bits_2_output), .\output (\xor ));
  nand_4bits nand_4bits_1 (
    .\input (registrador_4bits_1_output), .input_2(registrador_4bits_2_output), .\output (\nand ));
  nor_4bits nor_4bits_1 (.\input (registrador_4bits_1_output), .input_2(registrador_4bits_2_output), .\output (\nor ));
  xnor_4bits xnor_4bits_1 (
    .\input (registrador_4bits_1_output), .input_2(registrador_4bits_2_output), .\output (\xnor ));
  comparador_4bits comparador_4bits_1 (
    .\input (registrador_4bits_1_output), .input_2(registrador_4bits_2_output), .maior(maior), .igual(igual),
    .menor(menor));

  // Notes on the sheet:
  //   Nome: Daniel Sathler Silva, Mat: 405795
endmodule

module registrador_4bits (
  input  Clock,
  input  [3:0] Input,
  input  [3:0] Enabled,
  output [3:0] Output
);

  D_Flip_Flop #(.trigger("rising")) d_ff_1 (
    .clk(Clock), .D(Input[0]), .Q(Output[0]), .preset(Enabled[0]), .en(Enabled[0]));  // open: Qn, reset
  D_Flip_Flop #(.trigger("rising")) d_ff_2 (
    .clk(Clock), .D(Input[1]), .Q(Output[1]), .en(Enabled[1]));  // open: Qn, preset, reset
  D_Flip_Flop #(.trigger("rising")) d_ff_3 (
    .clk(Clock), .D(Input[2]), .Q(Output[2]), .en(Enabled[2]));  // open: Qn, preset, reset
  D_Flip_Flop #(.trigger("rising")) d_ff_4 (
    .clk(Clock), .D(Input[3]), .Q(Output[3]), .en(Enabled[3]));  // open: Qn, preset, reset

  // Notes on the sheet:
  //   Nome: Daniel Sathler Silva, Mat: 405795
endmodule

module and_4bits (
  input  [3:0] \input ,
  input  [3:0] input_2,
  output [3:0] \output 
);

  assign \output  = \input  & input_2;  // AND_Gate and_1, 4 bits wide

  // Notes on the sheet:
  //   Nome: Daniel Sathler Silva, Mat: 405795
endmodule

module or_4bits (
  input  [3:0] \input ,
  input  [3:0] input_2,
  output [3:0] \output 
);

  assign \output  = \input  | input_2;  // OR_Gate or_1, 4 bits wide

  // Notes on the sheet:
  //   Nome: Daniel Sathler Silva, Mat: 405795
endmodule

module not_4bits (
  input  [3:0] \input ,
  output [3:0] \output 
);

  assign \output  = ~\input ;  // NOT_Gate not_1, 4 bits wide

  // Notes on the sheet:
  //   Nome: Daniel Sathler Silva, Mat: 405795
endmodule

module xor_4bits (
  input  [3:0] \input ,
  input  [3:0] input_2,
  output [3:0] \output 
);

  assign \output  = \input  ^ input_2;  // XOR_Gate xor_1, 4 bits wide

  // Notes on the sheet:
  //   Nome: Daniel Sathler Silva, Mat: 405795
endmodule

module nand_4bits (
  input  [3:0] \input ,
  input  [3:0] input_2,
  output [3:0] \output 
);

  assign \output  = ~(\input  & input_2);  // NAND_Gate nand_1, 4 bits wide

  // Notes on the sheet:
  //   Nome: Daniel Sathler Silva, Mat: 405795
endmodule

module nor_4bits (
  input  [3:0] \input ,
  input  [3:0] input_2,
  output [3:0] \output 
);

  assign \output  = ~(\input  | input_2);  // NOR_Gate nor_1, 4 bits wide

  // Notes on the sheet:
  //   Nome: Daniel Sathler Silva, Mat: 405795
endmodule

module xnor_4bits (
  input  [3:0] \input ,
  input  [3:0] input_2,
  output [3:0] \output 
);

  assign \output  = ~(\input  ^ input_2);  // XNOR_Gate xnor_1, 4 bits wide

  // Notes on the sheet:
  //   Nome: Daniel Sathler Silva, Mat: 405795
endmodule

module comparador_4bits (
  input  [3:0] \input ,
  input  [3:0] input_2,
  output maior,
  output igual,
  output menor
);

  Comparator #(.width(4), .mode("twosComplement")) comparator_1 (
    .a(\input ), .b(input_2), .gt(maior), .eq(igual), .lt(menor));

  // Notes on the sheet:
  //   Nome: Daniel Sathler Silva, Mat: 405795
endmodule
