// Logisim project guia_13.circ as structural Verilog: 3 circuits, main circuit main
module main (
  input  data_a,
  input  data_b,
  input  [1:0] control,
  output out_4,
  output out_5,
  output out_6,
  output out_7,
  output a_b,
  output a_b_2,
  output a__b,
  output a__b_2
);

  wire clock_1_out, d_ff_1_q, d_ff_2_q, d_ff_3_q, d_ff_4_q, d_ff_5_q, d_ff_6_q, d_ff_7_q, d_ff_8_q;

  Clock #(.highDuration(1), .lowDuration(1)) clock_1 (.out(clock_1_out));
  D_Flip_Flop #(.trigger("rising")) d_ff_1 (
    .clk(clock_1_out), .D(data_a), .Q(d_ff_1_q));  // open: Qn, preset, en, reset
  D_Flip_Flop #(.trigger("rising")) d_ff_2 (
    .clk(clock_1_out), .D(d_ff_1_q), .Q(d_ff_2_q));  // open: Qn, preset, en, reset
  D_Flip_Flop #(.trigger("rising")) d_ff_3 (
    .clk(clock_1_out), .D(d_ff_2_q), .Q(d_ff_3_q));  // open: Qn, preset, en, reset
  D_Flip_Flop #(.trigger("rising")) d_ff_4 (
    .clk(clock_1_out), .D(d_ff_3_q), .Q(d_ff_4_q));  // open: Qn, preset, en, reset
  D_Flip_Flop #(.trigger("rising")) d_ff_5 (
    .clk(clock_1_out), .D(data_b), .Q(d_ff_5_q));  // open: Qn, preset, en, reset
  D_Flip_Flop #(.trigger("rising")) d_ff_6 (
    .clk(clock_1_out), .D(d_ff_5_q), .Q(d_ff_6_q));  // open: Qn, preset, en, reset
  D_Flip_Flop #(.trigger("rising")) d_ff_7 (
    .clk(clock_1_out), .D(d_ff_6_q), .Q(d_ff_7_q));  // open: Qn, preset, en, reset
  D_Flip_Flop #(.trigger("rising")) d_ff_8 (
    .clk(clock_1_out), .D(d_ff_7_q), .Q(d_ff_8_q));  // open: Qn, preset, en, reset
  ex_01 ex_01_1 (.a(d_ff_1_q), .b(d_ff_8_q), .control(control), .\output (out_4));
  ex_01 ex_01_2 (.a(d_ff_2_q), .b(d_ff_7_q), .control(control), .\output (out_5));
  ex_01 ex_01_3 (.a(d_ff_3_q), .b(d_ff_6_q), .control(control), .\output (out_6));
  ex_01 ex_01_4 (.a(d_ff_8_q), .b(d_ff_5_q), .control(control), .\output (out_7));
  ex_03 ex_03_1 (
    .a3(d_ff_1_q), .b3(d_ff_2_q), .a2(d_ff_3_q), .b2(d_ff_4_q), .a1(d_ff_8_q), .b1(d_ff_7_q), .a0(d_ff_6_q),
    .b0(d_ff_5_q), .a_b(a_b), .a_b_2(a_b_2), .a_b_3(a__b), .a__b(a__b_2));

  // Notes on the sheet:
  //   José Erimá Fernandes Júnior 405807
endmodule

module ex_01 (
  input  a,
  input  b,
  input  [1:0] control,
  output \output 
);

  wire and_1_out, nand_1_out, or_1_out, or_2_out, xor_1_out;

  and and_1 (and_1_out, a, b);
  or or_1 (or_1_out, a, b);
  or or_2 (or_2_out, a, b);
  xor xor_1 (xor_1_out, a, b);
  nand nand_1 (nand_1_out, or_2_out, or_2_out);
  Multiplexer #(.select(2), .width(1)) multiplexer_1 (
    .in0(and_1_out), .in1(or_1_out), .in2(xor_1_out), .in3(nand_1_out), .out(\output ), .sel(control));
endmodule

module ex_03 (
  input  a3,
  input  b3,
  input  a2,
  input  b2,
  input  a1,
  input  b1,
  input  a0,
  input  b0,
  output a_b,
  output a_b_2,
  output a_b_3,
  output a__b
);

  wire and_1_out, and_2_out, and_3_out, and_4_out, and_5_out, and_6_out, and_7_out, and_8_out, and_9_out,
       and_10_out, and_11_out, and_12_out, and_13_out, and_14_out, nor_1_out, nor_2_out, nor_3_out,
       nor_4_out, not_1_out, not_2_out, not_3_out, not_4_out, not_5_out, not_6_out, not_7_out, not_8_out;

  not not_1 (not_1_out, a3);
  not not_2 (not_2_out, b3);
  not not_3 (not_3_out, a2);
  not not_4 (not_4_out, b2);
  not not_5 (not_5_out, a1);
  not not_6 (not_6_out, b1);
  not not_7 (not_7_out, a0);
  not not_8 (not_8_out, b0);
  and and_1 (and_1_out, not_1_out, b3);
  and and_2 (and_2_out, a3, not_2_out);
  and and_3 (and_3_out, not_3_out, b2);
  and and_4 (and_4_out, a2, not_4_out);
  and and_5 (and_5_out, not_5_out, b1);
  and and_6 (and_6_out, a1, not_6_out);
  and and_7 (and_7_out, not_7_out, b0);
  and and_8 (and_8_out, a0, not_8_out);
  nor nor_1 (nor_1_out, and_1_out, and_2_out);
  nor nor_2 (nor_2_out, and_3_out, and_4_out);
  nor nor_3 (nor_3_out, and_5_out, and_6_out);
  nor nor_4 (nor_4_out, and_7_out, and_8_out);
  and and_9 (and_9_out, nor_1_out, and_3_out);
  and and_10 (and_10_out, nor_1_out, and_4_out);
  and and_11 (and_11_out, nor_1_out, and_5_out, nor_2_out);
  and and_12 (and_12_out, nor_1_out, and_6_out, nor_2_out);
  and and_13 (and_13_out, nor_1_out, and_7_out, nor_2_out, nor_3_out);
  and and_14 (and_14_out, nor_1_out, and_8_out, nor_2_out, nor_3_out);
  and and_15 (a_b_3, nor_1_out, nor_2_out, nor_3_out, nor_4_out);
  not not_9 (a__b, a_b_3);
  or or_1 (a_b, and_1_out, and_9_out, and_11_out, and_13_out);
  or or_2 (a_b_2, and_2_out, and_10_out, and_12_out, and_14_out);
endmodule
