// Logisim project Guia13.circ as structural Verilog: 9 circuits, main circuit Guia1305
module Guia1305 (
  input  [3:0] Instruction,
  input  R_W,
  input  [3:0] A,
  input  [3:0] B,
  input  CLK,
  input  CLR,
  output [3:0] Out0,
  output Out1
);

  wire [3:0] controlled_buffer_1_out, or_1_out, register_1_q, register_2_q, register_3_q;

  assign controlled_buffer_1_out = R_W ? Out0 : 4'bz;  // Controlled_Buffer controlled_buffer_1
  assign or_1_out = controlled_buffer_1_out | A;  // OR_Gate or_1, 4 bits wide
  Register #(.width(4), .trigger("rising")) register_1 (
    .D(Instruction), .en(1'b1), .Q(register_1_q), .clk(CLK), .clr(CLR));
  Register #(.width(4), .trigger("rising")) register_2 (
    .D(or_1_out), .en(1'b1), .Q(register_2_q), .clk(CLK), .clr(CLR));
  Register #(.width(4), .trigger("rising")) register_3 (.D(B), .en(1'b1), .Q(register_3_q), .clk(CLK), .clr(CLR));
  LU___4bits lu_4bits_1 (.Instruction(register_1_q), .A(register_2_q), .B(register_3_q), .Out0(Out0), .Out1(Out1));

  // Notes on the sheet:
  //   Luiz Felipe Fonseca - 405817
  //   0000 - Buffer
  //   0001 - not (A)
  //   0010 - or (A,B)
  //   0011 - and(A,B)
  //   0100 - xor(A,B)
  //   0101 - nand(A,B)
  //   0110 - nor(A,B)
  //   0111 - xnor(A,B)
  //   1000 - A < B
  //   1001 - A = B
  //   1010 - A > B
endmodule

module LU___4bits (
  input  [3:0] Instruction,
  input  [3:0] A,
  input  [3:0] B,
  output [3:0] Out0,
  output Out1
);

  wire comparator_1_eq, comparator_1_gt, comparator_1_lt;
  wire [2:0] demultiplexer_1_out0, demultiplexer_1_out1;
  wire [3:0] and_1_out, nand_1_out, nor_1_out, not_1_out, or_1_out, xnor_1_out, xor_1_out;

  assign not_1_out = ~A;  // NOT_Gate not_1, 4 bits wide
  Demultiplexer #(.select(1), .width(3), .tristate("false")) demultiplexer_1 (
    .out0(demultiplexer_1_out0), .out1(demultiplexer_1_out1), .in(Instruction[2:0]), .sel(Instruction[3]));
  assign or_1_out = A | B;  // OR_Gate or_1, 4 bits wide
  assign and_1_out = A & B;  // AND_Gate and_1, 4 bits wide
  assign xor_1_out = A ^ B;  // XOR_Gate xor_1, 4 bits wide
  assign nand_1_out = ~(A & B);  // NAND_Gate nand_1, 4 bits wide
  assign nor_1_out = ~(A | B);  // NOR_Gate nor_1, 4 bits wide
  assign xnor_1_out = ~(A ^ B);  // XNOR_Gate xnor_1, 4 bits wide
  Comparator #(.width(4), .mode("twosComplement")) comparator_1 (
    .a(A), .b(B), .gt(comparator_1_gt), .eq(comparator_1_eq), .lt(comparator_1_lt));
  Multiplexer #(.select(3), .width(4)) multiplexer_1 (
    .in0(A), .in1(not_1_out), .in2(or_1_out), .in3(and_1_out), .in4(xor_1_out), .in5(nand_1_out),
    .in6(nor_1_out), .in7(xnor_1_out), .out(Out0), .sel(demultiplexer_1_out0));
  Multiplexer #(.select(3), .width(1)) multiplexer_2 (
    .in0(1'b0), .in1(comparator_1_gt), .in2(comparator_1_eq), .in3(comparator_1_lt), .in4(1'b0), .in5(1'b0),
    .in6(1'b0), .in7(1'b0), .out(Out1), .sel(demultiplexer_1_out1));

  // Notes on the sheet:
  //   0000 - Buffer
  //   0001 - not (A)
  //   0010 - or (A,B)
  //   0011 - and(A,B)
  //   0100 - xor(A,B)
  //   0101 - nand(A,B)
  //   0110 - nor(A,B)
  //   0111 - xnor(A,B)
  //   1001 - A < B
  //   1010 - A = B
  //   1011 - A > B
  //   Luiz Felipe Fonseca - 405817
endmodule

module LU___2bits (
  input  [2:0] Instruction,
  input  [1:0] A,
  input  [1:0] B,
  output [1:0] Out0
);

  wire [1:0] and_1_out, not_1_out, or_1_out, xor_1_out;

  assign not_1_out = ~A;  // NOT_Gate not_1, 2 bits wide
  assign or_1_out = A | B;  // OR_Gate or_1, 2 bits wide
  assign and_1_out = A & B;  // AND_Gate and_1, 2 bits wide
  assign xor_1_out = A ^ B;  // XOR_Gate xor_1, 2 bits wide
  Multiplexer #(.select(3), .width(2)) multiplexer_1 (
    .in0(A), .in1(not_1_out), .in2(or_1_out), .in3(and_1_out), .in4(xor_1_out), .in5(2'b00), .in6(2'b00),
    .in7(2'b00), .out(Out0), .sel(Instruction));

  // Notes on the sheet:
  //   000 - Buffer
  //   001 - not (A)
  //   010 - or (A,B)
  //   011 -and(A, B)
  //   100 - xor(A,B)
  //   Luiz Felipe Fonseca - 405817
endmodule

module Guia1301 (
  input  [2:0] Instruction,
  input  [1:0] R_W,
  input  [1:0] A,
  input  [1:0] B,
  input  CLEAR,
  input  CLK,
  output [1:0] Output
);

  wire [1:0] and_1_out, or_1_out, register_3_q, register_4_q;
  wire [2:0] register_5_q;

  Register #(.width(1), .trigger("rising")) register_1 (
    .D(Instruction[2]), .Q(register_5_q[2]), .clk(CLK), .clr(CLEAR));  // open: en
  assign and_1_out = Output & R_W;  // AND_Gate and_1, 2 bits wide
  assign or_1_out = and_1_out | A;  // OR_Gate or_1, 2 bits wide
  Register #(.width(1), .trigger("rising")) register_2 (
    .D(Instruction[1]), .Q(register_5_q[1]), .clk(CLK), .clr(CLEAR));  // open: en
  Register #(.width(2), .trigger("rising")) register_3 (
    .D(or_1_out), .Q(register_3_q), .clk(CLK), .clr(CLEAR));  // open: en
  LU___2bits lu_2bits_1 (.Instruction(register_5_q), .A(register_3_q), .B(register_4_q), .Out0(Output));
  Register #(.width(2), .trigger("rising")) register_4 (.D(B), .Q(register_4_q), .clk(CLK), .clr(CLEAR));  // open: en
  Register #(.width(1), .trigger("rising")) register_5 (
    .D(Instruction[0]), .Q(register_5_q[0]), .clk(CLK), .clr(CLEAR));  // open: en

  // Notes on the sheet:
  //   000 - Buffer
  //   001 - not (A)
  //   010 - or (A,B)
  //   011 -and(A, B)
  //   100 - xor(A,B)
  //   Luiz Felipe Fonseca - 405817
endmodule

module Guia1304 (
  input  [3:0] Instruction,
  input  R_W,
  input  [3:0] A,
  input  [3:0] B,
  input  CLK,
  input  CLR,
  output [3:0] Out0,
  output Out1
);

  wire [3:0] controlled_buffer_1_out, or_1_out, register_1_q, register_2_q, register_3_q;

  assign controlled_buffer_1_out = R_W ? Out0 : 4'bz;  // Controlled_Buffer controlled_buffer_1
  assign or_1_out = controlled_buffer_1_out | A;  // OR_Gate or_1, 4 bits wide
  Register #(.width(4), .trigger("rising")) register_1 (
    .D(Instruction), .en(1'b1), .Q(register_1_q), .clk(CLK), .clr(CLR));
  Register #(.width(4), .trigger("rising")) register_2 (
    .D(or_1_out), .en(1'b1), .Q(register_2_q), .clk(CLK), .clr(CLR));
  Register #(.width(4), .trigger("rising")) register_3 (.D(B), .en(1'b1), .Q(register_3_q), .clk(CLK), .clr(CLR));
  LU___4bits lu_4bits_1 (.Instruction(register_1_q), .A(register_2_q), .B(register_3_q), .Out0(Out0), .Out1(Out1));

  // Notes on the sheet:
  //   Luiz Felipe Fonseca - 405817
  //   0000 - Buffer
  //   0001 - not (A)
  //   0010 - or (A,B)
  //   0011 - and(A,B)
  //   0100 - xor(A,B)
  //   0101 - nand(A,B)
  //   0110 - nor(A,B)
  //   0111 - xnor(A,B)
  //   1000 - A < B
  //   1001 - A = B
  //   1010 - A > B
endmodule

module Guia1302 (
  input  [2:0] Instruction,
  input  [1:0] R_W,
  input  [1:0] A,
  input  [1:0] B,
  input  CLEAR,
  input  CLK,
  output [1:0] Output
);

  wire [1:0] and_1_out, or_1_out, register_3_q, register_4_q;
  wire [2:0] register_5_q;

  Register #(.width(1), .trigger("rising")) register_1 (
    .D(Instruction[2]), .Q(register_5_q[2]), .clk(CLK), .clr(CLEAR));  // open: en
  assign and_1_out = Output & R_W;  // AND_Gate and_1, 2 bits wide
  assign or_1_out = and_1_out | A;  // OR_Gate or_1, 2 bits wide
  Register #(.width(1), .trigger("rising")) register_2 (
    .D(Instruction[1]), .Q(register_5_q[1]), .clk(CLK), .clr(CLEAR));  // open: en
  Register #(.width(2), .trigger("rising")) register_3 (
    .D(or_1_out), .Q(register_3_q), .clk(CLK), .clr(CLEAR));  // open: en
  LU___2bits_b lu_2bits_b_1 (.Instruction(register_5_q), .A(register_3_q), .B(register_4_q), .Out0(Output));
  Register #(.width(2), .trigger("rising")) register_4 (.D(B), .Q(register_4_q), .clk(CLK), .clr(CLEAR));  // open: en
  Register #(.width(1), .trigger("rising")) register_5 (
    .D(Instruction[0]), .Q(register_5_q[0]), .clk(CLK), .clr(CLEAR));  // open: en

  // Notes on the sheet:
  //   000 - Buffer
  //   001 - not (A)
  //   010 - or (A,B)
  //   011 -and(A, B)
  //   100 - xor(A,B)
  //   101 - nand (A,B)
  //   110 - nor (A,B)
  //   111 - xnor (A,B)
  //   Luiz Felipe Fonseca - 405817
endmodule

module LU___2bits_b (
  input  [2:0] Instruction,
  input  [1:0] A,
  input  [1:0] B,
  output [1:0] Out0
);

  wire [1:0] and_1_out, nand_1_out, nor_1_out, not_1_out, or_1_out, xnor_1_out, xor_1_out;

  assign not_1_out = ~A;  // NOT_Gate not_1, 2 bits wide
  assign or_1_out = A | B;  // OR_Gate or_1, 2 bits wide
  assign and_1_out = A & B;  // AND_Gate and_1, 2 bits wide
  assign xor_1_out = A ^ B;  // XOR_Gate xor_1, 2 bits wide
  assign nand_1_out = ~(A & B);  // NAND_Gate nand_1, 2 bits wide
  assign nor_1_out = ~(A | B);  // NOR_Gate nor_1, 2 bits wide
  assign xnor_1_out = ~(A ^ B);  // XNOR_Gate xnor_1, 2 bits wide
  Multiplexer #(.select(3), .width(2)) multiplexer_1 (
    .in0(A), .in1(not_1_out), .in2(or_1_out), .in3(and_1_out), .in4(xor_1_out), .in5(nand_1_out),
    .in6(nor_1_out), .in7(xnor_1_out), .out(Out0), .sel(Instruction));

  // Notes on the sheet:
  //   000 - Buffer
  //   001 - not (A)
  //   010 - or (A,B)
  //   011 -and(A, B)
  //   100 - xor(A,B)
  //   101 - nand (A,B)
  //   110 - nor (A,B)
  //   111 - xnor (A,B)
  //   Luiz Felipe Fonseca - 405817
endmodule

module Guia1303 (
  input  [3:0] Instruction,
  input  [1:0] R_W,
  input  [1:0] A,
  input  [1:0] B,
  input  CLEAR,
  input  CLK,
  output [1:0] Output
);

  wire [1:0] and_1_out, or_1_out, register_3_q, register_4_q;
  wire [3:0] register_6_q;

  Register #(.width(1), .trigger("rising")) register_1 (
    .D(Instruction[3]), .Q(register_6_q[3]), .clk(CLK), .clr(CLEAR));  // open: en
  assign and_1_out = Output & R_W;  // AND_Gate and_1, 2 bits wide
  assign or_1_out = and_1_out | A;  // OR_Gate or_1, 2 bits wide
  Register #(.width(1), .trigger("rising")) register_2 (
    .D(Instruction[2]), .Q(register_6_q[2]), .clk(CLK), .clr(CLEAR));  // open: en
  LU___2bits_c lu_2bits_c_1 (
    .Instruction(register_6_q), .A(register_3_q), .B(register_4_q), .Out0(Output));  // open: Out0_2
  Register #(.width(2), .trigger("rising")) register_3 (
    .D(or_1_out), .Q(register_3_q), .clk(CLK), .clr(CLEAR));  // open: en
  Register #(.width(2), .trigger("rising")) register_4 (.D(B), .Q(register_4_q), .clk(CLK), .clr(CLEAR));  // open: en
  Register #(.width(1), .trigger("rising")) register_5 (
    .D(Instruction[1]), .Q(register_6_q[1]), .clk(CLK), .clr(CLEAR));  // open: en
  Register #(.width(1), .trigger("rising")) register_6 (
    .D(Instruction[0]), .Q(register_6_q[0]), .clk(CLK), .clr(CLEAR));  // open: en

  // Notes on the sheet:
  //   Luiz Felipe Fonseca - 405817
  //   0000 - Buffer
  //   0001 - not (A)
  //   0010 - or (A,B)
  //   0011 -and(A, B)
  //   0100 - xor(A,B)
  //   0101 - nand (A,B)
  //   0110 - nor (A,B)
  //   0111 - xnor (A,B)
  //   1000 - A<B
  //   1001 - A=B
  //   1010 - A>B
endmodule

module LU___2bits_c (
  input  [3:0] Instruction,
  input  [1:0] A,
  input  [1:0] B,
  output [1:0] Out0,
  output Out0_2
);

  wire comparator_1_eq, comparator_1_gt, comparator_1_lt;
  wire [1:0] and_1_out, nand_1_out, nor_1_out, not_1_out, or_1_out, xnor_1_out, xor_1_out;
  wire [2:0] demultiplexer_1_out0, demultiplexer_1_out1, undriven;

  assign not_1_out = ~A;  // NOT_Gate not_1, 2 bits wide
  Demultiplexer #(.select(1), .width(3), .tristate("false")) demultiplexer_1 (
    .out0(demultiplexer_1_out0), .out1(demultiplexer_1_out1), .in(undriven), .sel(Instruction[3]));
  assign or_1_out = A | B;  // OR_Gate or_1, 2 bits wide
  assign and_1_out = A & B;  // AND_Gate and_1, 2 bits wide
  assign xor_1_out = A ^ B;  // XOR_Gate xor_1, 2 bits wide
  assign nand_1_out = ~(A & B);  // NAND_Gate nand_1, 2 bits wide
  assign nor_1_out = ~(A | B);  // NOR_Gate nor_1, 2 bits wide
  assign xnor_1_out = ~(A ^ B);  // XNOR_Gate xnor_1, 2 bits wide
  Comparator #(.width(2), .mode("twosComplement")) comparator_1 (
    .a(A), .b(B), .gt(comparator_1_gt), .eq(comparator_1_eq), .lt(comparator_1_lt));
  Multiplexer #(.select(3), .width(2)) multiplexer_1 (
    .in0(A), .in1(not_1_out), .in2(or_1_out), .in3(and_1_out), .in4(xor_1_out), .in5(nand_1_out),
    .in6(nor_1_out), .in7(xnor_1_out), .out(Out0), .sel(demultiplexer_1_out0));
  Multiplexer #(.select(3), .width(1)) multiplexer_2 (
    .in0(comparator_1_gt), .in1(comparator_1_eq), .in2(comparator_1_lt), .in3(1'b0), .in4(1'b0), .in5(1'b0),
    .in6(1'b0), .in7(1'b0), .out(Out0_2), .sel(demultiplexer_1_out1));

  // Notes on the sheet:
  //   0000 - Buffer
  //   0001 - not (A)
  //   0010 - or (A,B)
  //   0011 -and(A, B)
  //   0100 - xor(A,B)
  //   0101 - nand (A,B)
  //   0110 - nor (A,B)
  //   0111 - xnor (A,B)
  //   1000 - A< B
  //   1001 - A=B
  //   1010 - A>B
  //   Luiz Felipe Fonseca - 405817
endmodule
