// Logisim project Numeros_01_02_e_03.circ as structural Verilog: 6 circuits, main circuit main
module main (
  input  [1:0] data,
  input  [1:0] B,
  input  [5:0] datapath,
  input  [3:0] chave,
  output [1:0] saida
);

  wire clock_out;

  Clock #(.highDuration(1), .lowDuration(1)) clock (.out(clock_out));
  LU_2bits lu_2bits_1 (.clock(clock_out), .A(data), .B(B), .datapath(datapath), .chave(chave), .saida(saida));

  // Notes on the sheet:
  //   A
  //   leAleBleO
  //   CHAVE             SAIDA
  //   0000
  //   0001
  //   0010
  //   0011
  //   0100
  //   0101
  //   0110
  //   0111
  //   1000
  //   1001
  //   1010
  //   not A
  //   A and B
  //   A or B
  //   A xor B
  //   not B
  //   A nand B
  //   A nor B
  //   A xnor B
  //   A < B
  //   A = B
  //   A > B
endmodule

module LU_2bits (
  input  clock,
  input  [1:0] A,
  input  [1:0] B,
  input  [5:0] datapath,
  input  [3:0] chave,
  output [1:0] saida
);

  wire [1:0] a_b_1_saida, a_b_2_saida, a_b_3_saida, and_1_out, multiplexer_1_out, nand_1_out, nor_1_out,
       not_1_out, not_2_out, or_1_out, registrador_1_saida, registrador_2_saida, xnor_1_out, xor_1_out;

  registrador registrador_1 (
    .clock(clock), .load(datapath[5]), .enable(datapath[4]), .entrada(A), .saida(registrador_1_saida));
  registrador registrador_2 (
    .clock(clock), .load(datapath[3]), .enable(datapath[2]), .entrada(B), .saida(registrador_2_saida));
  assign not_1_out = ~registrador_1_saida;  // NOT_Gate not_1, 2 bits wide
  A___B a_b_1 (.A(registrador_1_saida), .B(registrador_2_saida), .SAIDA(a_b_1_saida));
  A___B_2_2 a_b_2 (.A(registrador_1_saida), .B(registrador_2_saida), .SAIDA(a_b_2_saida));
  A___B_2 a_b_3 (.A(registrador_1_saida), .B(registrador_2_saida), .SAIDA(a_b_3_saida));
  assign and_1_out = registrador_1_saida & registrador_2_saida;  // AND_Gate and_1, 2 bits wide
  assign or_1_out = registrador_1_saida | registrador_2_saida;  // OR_Gate or_1, 2 bits wide
  assign xor_1_out = registrador_1_saida ^ registrador_2_saida;  // XOR_Gate xor_1, 2 bits wide
  assign not_2_out = ~registrador_2_saida;  // NOT_Gate not_2, 2 bits wide
  assign nand_1_out = ~(registrador_1_saida & registrador_2_saida);  // NAND_Gate nand_1, 2 bits wide
  assign nor_1_out = ~(registrador_1_saida | registrador_2_saida);  // NOR_Gate nor_1, 2 bits wide
  assign xnor_1_out = ~(registrador_1_saida ^ registrador_2_saida);  // XNOR_Gate xnor_1, 2 bits wide
  Multiplexer #(.select(4), .width(2)) multiplexer_1 (
    .in0(not_1_out), .in1(and_1_out), .in2(or_1_out), .in3(xor_1_out), .in4(not_2_out), .in5(nand_1_out),
    .in6(nor_1_out), .in7(xnor_1_out), .in8(a_b_1_saida), .in9(a_b_2_saida), .in10(a_b_3_saida),
    .out(multiplexer_1_out), .sel(chave));  // open: in11, in12, in13, in14, in15
  registrador registrador_3 (
    .clock(clock), .load(datapath[1]), .enable(datapath[0]), .entrada(multiplexer_1_out), .saida(saida));

  // Notes on the sheet:
  //   leAleBleO
  //   A < B
  //   A = B
  //   A > B
endmodule

module A___B (
  input  [1:0] A,
  input  [1:0] B,
  output [1:0] SAIDA
);

  wire and_1_out, and_2_out, and_3_out, and_4_out, and_5_out, and_6_out, not_1_out, not_2_out, not_3_out,
       not_4_out, not_5_out, not_6_out, not_7_out, not_8_out, not_9_out, not_10_out, not_11_out, not_12_out;

  not not_1 (not_1_out, A[1]);
  not not_2 (not_2_out, A[0]);
  not not_3 (not_3_out, B[1]);
  not not_4 (not_4_out, A[1]);
  not not_5 (not_5_out, A[0]);
  not not_6 (not_6_out, B[0]);
  not not_7 (not_7_out, A[1]);
  not not_8 (not_8_out, B[0]);
  not not_9 (not_9_out, A[1]);
  not not_10 (not_10_out, A[0]);
  not not_11 (not_11_out, A[1]);
  not not_12 (not_12_out, A[0]);
  and and_1 (and_1_out, not_1_out, not_2_out, B[0], not_3_out);
  and and_2 (and_2_out, not_4_out, not_5_out, B[1], not_6_out);
  and and_3 (and_3_out, not_7_out, A[0], B[1], not_8_out);
  and and_4 (and_4_out, not_9_out, not_10_out, B[1], B[0]);
  and and_5 (and_5_out, not_11_out, A[0], B[1], B[0]);
  and and_6 (and_6_out, A[1], not_12_out, B[1], B[0]);
  or or_1 (SAIDA[1], and_1_out, and_2_out, and_3_out, and_4_out, and_5_out, and_6_out);

  assign SAIDA[0] = SAIDA[1];

  // Notes on the sheet:
  //   comparador A < B
endmodule

module A___B_2 (
  input  [1:0] A,
  input  [1:0] B,
  output [1:0] SAIDA
);

  wire and_1_out, and_2_out, and_3_out, and_4_out, and_5_out, and_6_out, not_1_out, not_2_out, not_3_out,
       not_4_out, not_5_out, not_6_out, not_7_out, not_8_out, not_9_out, not_10_out, not_11_out, not_12_out;

  not not_1 (not_1_out, B[1]);
  not not_2 (not_2_out, B[1]);
  not not_3 (not_3_out, B[1]);
  not not_4 (not_4_out, B[0]);
  not not_5 (not_5_out, A[1]);
  not not_6 (not_6_out, B[0]);
  not not_7 (not_7_out, B[1]);
  not not_8 (not_8_out, A[0]);
  not not_9 (not_9_out, B[1]);
  not not_10 (not_10_out, B[0]);
  not not_11 (not_11_out, B[0]);
  not not_12 (not_12_out, A[0]);
  and and_1 (and_1_out, not_5_out, A[0], not_6_out, not_7_out);
  and and_2 (and_2_out, A[1], not_8_out, not_9_out, not_10_out);
  and and_3 (and_3_out, A[1], A[0], not_1_out, not_11_out);
  and and_4 (and_4_out, A[1], not_12_out, not_2_out, B[0]);
  and and_5 (and_5_out, A[1], A[0], not_3_out, B[0]);
  and and_6 (and_6_out, A[1], A[0], B[1], not_4_out);
  or or_1 (SAIDA[1], and_1_out, and_2_out, and_3_out, and_4_out, and_5_out, and_6_out);

  assign SAIDA[0] = SAIDA[1];

  // Notes on the sheet:
  //   comparador A > B
endmodule

module A___B_2_2 (
  input  [1:0] A,
  input  [1:0] B,
  output [1:0] SAIDA
);

  wire and_1_out, and_2_out, and_3_out, and_4_out, not_1_out, not_2_out, not_3_out, not_4_out, not_5_out,
       not_6_out, not_7_out, not_8_out;

  not not_1 (not_1_out, A[1]);
  not not_2 (not_2_out, A[0]);
  not not_3 (not_3_out, B[0]);
  not not_4 (not_4_out, B[1]);
  not not_5 (not_5_out, A[0]);
  not not_6 (not_6_out, B[0]);
  not not_7 (not_7_out, A[1]);
  not not_8 (not_8_out, B[1]);
  and and_1 (and_1_out, not_1_out, not_2_out, not_3_out, not_4_out);
  and and_2 (and_2_out, A[1], not_5_out, B[1], not_6_out);
  and and_3 (and_3_out, A[1], A[0], B[1], B[0]);
  and and_4 (and_4_out, not_7_out, A[0], not_8_out, B[0]);
  or or_1 (SAIDA[1], and_2_out, and_1_out, and_3_out, and_4_out);

  assign SAIDA[0] = SAIDA[1];

  // Notes on the sheet:
  //   comparador A = B
endmodule

module registrador (
  input  clock,
  input  [1:0] entrada,
  input  load,
  input  enable,
  output [1:0] saida
);

  wire controlled_buffer_1_out, controlled_buffer_2_out;

  assign controlled_buffer_1_out = load ? entrada[0] : 1'bz;  // Controlled_Buffer controlled_buffer_1
  assign controlled_buffer_2_out = load ? entrada[1] : 1'bz;  // Controlled_Buffer controlled_buffer_2
  D_Flip_Flop #(.trigger("rising")) d_ff_1 (
    .clk(clock), .D(controlled_buffer_1_out), .Q(saida[0]), .en(enable));  // open: Qn, preset, reset
  D_Flip_Flop #(.trigger("rising")) d_ff_2 (
    .clk(clock), .D(controlled_buffer_2_out), .Q(saida[1]), .en(enable));  // open: Qn, preset, reset

  // Notes on the sheet:
  //   bit 0
  //   bit 1
endmodule
