// Logisim project Numeros_04_e_05.circ as structural Verilog: 6 circuits, main circuit main
module main (
  input  [3:0] data,
  input  [3:0] B,
  input  [5:0] datapath,
  input  [3:0] chave,
  output [3:0] saida
);

  wire clock_out;

  Clock #(.highDuration(1), .lowDuration(1)) clock (.out(clock_out));
  LU_4bits lu_4bits_1 (.clock(clock_out), .A(data), .B(B), .datapath(datapath), .chave(chave), .saida(saida));

  // Notes on the sheet:
  //   A
  //   leAleBleO
  //   CHAVE             SAIDA
  //   0000
  //   0001
  //   0010
  //   0011
  //   0100
  //   0101
  //   0110
  //   0111
  //   1000
  //   1001
  //   1010
  //   not A
  //   A and B
  //   A or B
  //   A xor B
  //   not B
  //   A nand B
  //   A nor B
  //   A xnor B
  //   A < B
  //   A = B
  //   A > B
  //   nao está funcionando
  //   nao está funcionando
  //   nao está funcionando
endmodule

module LU_4bits (
  input  clock,
  input  [3:0] A,
  input  [3:0] B,
  input  [5:0] datapath,
  input  [3:0] chave,
  output [3:0] saida
);

  wire [3:0] and_1_out, multiplexer_1_out, nand_1_out, nor_1_out, not_1_out, not_2_out, or_1_out,
       registrador_1_saida, registrador_2_saida, undriven, undriven_2, undriven_3, xnor_1_out, xor_1_out;

  registrador registrador_1 (
    .clock(clock), .load(datapath[5]), .enable(datapath[4]), .entrada(A), .saida(registrador_1_saida));
  registrador registrador_2 (
    .clock(clock), .load(datapath[3]), .enable(datapath[2]), .entrada(B), .saida(registrador_2_saida));
  assign not_1_out = ~registrador_1_saida;  // NOT_Gate not_1, 4 bits wide
  assign and_1_out = registrador_1_saida & registrador_2_saida;  // AND_Gate and_1, 4 bits wide
  assign or_1_out = registrador_1_saida | registrador_2_saida;  // OR_Gate or_1, 4 bits wide
  assign xor_1_out = registrador_1_saida ^ registrador_2_saida;  // XOR_Gate xor_1, 4 bits wide
  assign not_2_out = ~registrador_2_saida;  // NOT_Gate not_2, 4 bits wide
  assign nand_1_out = ~(registrador_1_saida & registrador_2_saida);  // NAND_Gate nand_1, 4 bits wide
  assign nor_1_out = ~(registrador_1_saida | registrador_2_saida);  // NOR_Gate nor_1, 4 bits wide
  assign xnor_1_out = ~(registrador_1_saida ^ registrador_2_saida);  // XNOR_Gate xnor_1, 4 bits wide
  Multiplexer #(.select(4), .width(4)) multiplexer_1 (
    .in0(not_1_out), .in1(and_1_out), .in2(or_1_out), .in3(xor_1_out), .in4(not_2_out), .in5(nand_1_out),
    .in6(nor_1_out), .in7(xnor_1_out), .in8(undriven), .in9(undriven_2), .in10(undriven_3),
    .out(multiplexer_1_out), .sel(chave));  // open: in11, in12, in13, in14, in15
  registrador registrador_3 (
    .clock(clock), .load(datapath[1]), .enable(datapath[0]), .entrada(multiplexer_1_out), .saida(saida));

  // Notes on the sheet:
  //   leAleBleO
endmodule

module A___B (
  input  [3:0] entrada_A,
  input  [3:0] entrada_B,
  output [3:0] saida
);

  wire and_1_out, and_2_out, and_3_out, and_4_out, and_5_out, and_6_out, and_7_out, and_8_out, and_9_out,
       and_10_out, and_11_out, and_12_out, and_13_out, and_14_out, and_15_out, and_16_out, and_17_out,
       and_18_out, and_19_out, not_1_out, not_2_out, not_3_out, not_4_out, not_5_out, not_6_out, not_7_out,
       not_8_out, or_1_out, or_2_out, or_3_out, or_4_out;

  not not_1 (not_1_out, entrada_A[0]);
  not not_2 (not_2_out, entrada_A[3]);
  not not_3 (not_3_out, entrada_A[1]);
  not not_4 (not_4_out, entrada_A[2]);
  not not_5 (not_5_out, entrada_B[2]);
  not not_6 (not_6_out, entrada_B[3]);
  not not_7 (not_7_out, entrada_B[0]);
  not not_8 (not_8_out, entrada_B[1]);
  and and_1 (and_1_out, not_1_out, not_3_out, not_4_out, not_2_out);
  and and_2 (and_2_out, entrada_A[0], not_3_out, not_4_out, not_2_out);
  and and_3 (and_3_out, not_1_out, not_3_out, not_4_out, not_2_out);
  and and_4 (and_4_out, entrada_A[0], not_3_out, not_4_out, not_2_out);
  and and_5 (and_5_out, entrada_A[1], not_1_out, not_4_out, not_2_out);
  and and_6 (and_6_out, not_1_out, not_3_out, not_4_out, not_2_out);
  and and_7 (and_7_out, entrada_A[0], not_3_out, not_4_out, not_2_out);
  and and_8 (and_8_out, entrada_A[1], not_1_out, not_4_out, not_2_out);
  and and_9 (and_9_out, entrada_A[0], entrada_A[1], not_4_out, not_2_out);
  and and_10 (and_10_out, not_1_out, not_3_out, not_4_out, not_2_out);
  and and_11 (and_11_out, entrada_A[0], not_3_out, not_4_out, not_2_out);
  and and_12 (and_12_out, entrada_A[1], not_1_out, not_4_out, not_2_out);
  and and_13 (and_13_out, entrada_A[0], entrada_A[1], not_4_out, not_2_out);
  and and_14 (and_14_out, entrada_A[2], not_1_out, not_3_out, not_2_out);
  and and_15 (and_15_out, not_1_out, not_3_out, not_4_out, not_2_out, entrada_B[0], not_8_out, not_5_out, not_6_out);
  or or_1 (or_1_out, and_1_out, and_2_out);
  or or_2 (or_2_out, and_3_out, and_4_out, and_5_out);
  and and_16 (and_16_out, or_2_out, entrada_B[0], entrada_B[1], not_5_out, not_6_out);
  or or_3 (or_3_out, and_6_out, and_7_out, and_8_out, and_9_out);
  and and_17 (and_17_out, or_3_out, entrada_B[2], not_7_out, not_8_out, not_6_out);
  and and_18 (and_18_out, or_4_out, entrada_B[2], entrada_B[0], not_7_out, not_6_out);
  and and_19 (and_19_out, or_1_out, entrada_B[1], not_7_out, not_5_out, not_6_out);
  or or_4 (or_4_out, and_10_out, and_11_out, and_12_out, and_13_out, and_14_out);
  // NOT_Gate not_9 is placed but not wired
  // AND_Gate and_20 is placed but not wired
  // OR_Gate or_5 is placed but not wired
endmodule

module A___B_2 (
  input  [3:0] entrada_A,
  input  [3:0] entrada_B
);

  wire not_1_out, not_2_out, not_3_out, not_4_out, not_5_out, not_6_out, not_7_out, not_8_out;

  not not_1 (not_1_out, entrada_A[2]);
  not not_2 (not_2_out, entrada_A[3]);
  not not_3 (not_3_out, entrada_A[0]);
  not not_4 (not_4_out, entrada_A[1]);
  not not_5 (not_5_out, entrada_B[0]);
  not not_6 (not_6_out, entrada_B[2]);
  not not_7 (not_7_out, entrada_B[1]);
  not not_8 (not_8_out, entrada_B[3]);
endmodule

module A___B_2_2 (
  input  [3:0] A,
  input  [3:0] B,
  output SAIDA
);

  wire and_1_out, and_2_out, and_3_out, and_4_out, not_1_out, not_2_out, not_3_out, not_4_out, not_5_out,
       not_6_out, not_7_out, not_8_out;

  not not_1 (not_1_out, A[1]);
  not not_2 (not_2_out, A[0]);
  not not_3 (not_3_out, B[0]);
  not not_4 (not_4_out, B[1]);
  not not_5 (not_5_out, A[0]);
  not not_6 (not_6_out, B[0]);
  not not_7 (not_7_out, A[1]);
  not not_8 (not_8_out, B[1]);
  and and_1 (and_1_out, not_1_out, not_2_out, not_3_out, not_4_out);
  and and_2 (and_2_out, A[1], not_5_out, B[1], not_6_out);
  and and_3 (and_3_out, A[1], A[0], B[1], B[0]);
  and and_4 (and_4_out, not_7_out, A[0], not_8_out, B[0]);
  or or_1 (SAIDA, and_2_out, and_1_out, and_3_out, and_4_out);

  // Notes on the sheet:
  //   comparador A = B
endmodule

module registrador (
  input  clock,
  input  [3:0] entrada,
  input  load,
  input  enable,
  output [3:0] saida
);

  wire controlled_buffer_1_out, controlled_buffer_2_out, controlled_buffer_3_out, controlled_buffer_4_out;

  assign controlled_buffer_1_out = load ? entrada[0] : 1'bz;  // Controlled_Buffer controlled_buffer_1
  assign controlled_buffer_2_out = load ? entrada[1] : 1'bz;  // Controlled_Buffer controlled_buffer_2
  assign controlled_buffer_3_out = load ? entrada[2] : 1'bz;  // Controlled_Buffer controlled_buffer_3
  assign controlled_buffer_4_out = load ? entrada[3] : 1'bz;  // Controlled_Buffer controlled_buffer_4
  D_Flip_Flop #(.trigger("rising")) d_ff_1 (
    .clk(clock), .D(controlled_buffer_1_out), .Q(saida[0]), .en(enable));  // open: Qn, preset, reset
  D_Flip_Flop #(.trigger("rising")) d_ff_2 (
    .clk(clock), .D(controlled_buffer_2_out), .Q(saida[1]), .en(enable));  // open: Qn, preset, reset
  D_Flip_Flop #(.trigger("rising")) d_ff_3 (
    .clk(clock), .D(controlled_buffer_3_out), .Q(saida[2]), .en(enable));  // open: Qn, preset, reset
  D_Flip_Flop #(.trigger("rising")) d_ff_4 (
    .clk(clock), .D(controlled_buffer_4_out), .Q(saida[3]), .en(enable));  // open: Qn, preset, reset

  // Notes on the sheet:
  //   bit 0
  //   bit 1
  //   bit 2
  //   bit 3
endmodule
