// Logisim project Guia13-405830.circ as structural Verilog: 10 circuits, main circuit RegD
module RegD (
  input  [1:0] in_1,
  input  CLK,
  output [1:0] out_3
);

  D_Flip_Flop #(.trigger("rising")) d_ff_1 (.clk(CLK), .D(in_1[0]), .Q(out_3[0]));  // open: Qn, preset, en, reset
  D_Flip_Flop #(.trigger("rising")) d_ff_2 (.clk(CLK), .D(in_1[1]), .Q(out_3[1]));  // open: Qn, preset, en, reset
endmodule

module RegNot (
  input  [1:0] in_1,
  output [1:0] out_2
);

  not not_1 (out_2[0], in_1[0]);
  not not_2 (out_2[1], in_1[1]);
endmodule

module RegAnd (
  input  [1:0] in_1,
  input  [1:0] in_2,
  output [1:0] out_3
);

  and and_1 (out_3[1], in_1[1], in_1[0]);
  and and_2 (out_3[0], in_2[1], in_2[0]);
endmodule

module RegOR (
  input  [1:0] in_1,
  input  [1:0] in_2,
  output [1:0] out_3
);

  or or_1 (out_3[1], in_1[1], in_1[0]);
  or or_2 (out_3[0], in_2[1], in_2[0]);
endmodule

module RegXnor (
  input  [1:0] in_1,
  input  [1:0] in_2,
  output [1:0] out_3
);

  xnor xnor_1 (out_3[1], in_1[1], in_1[0]);
  xnor xnor_2 (out_3[0], in_2[1], in_2[0]);
endmodule

module Guia13 (
  input  [1:0] in_1,
  input  in_2,
  input  [1:0] in_3,
  input  [3:0] in_4,
  output [1:0] out_5
);

  wire [1:0] comparador_1_out_3, comparador_1_out_4, comparador_1_out_5, regand_1_out_3, regd_1_out_3,
       regd_2_out_3, regnand_1_out_3, regnor_1_out_3, regnot_1_out_2, regnot_2_out_2, regor_1_out_3,
       regxnor_1_out_3, regxor_1_out_3;

  RegD regd_1 (.in_1(in_1), .CLK(in_2), .out_3(regd_1_out_3));
  RegNot regnot_1 (.in_1(regd_1_out_3), .out_2(regnot_1_out_2));
  RegD regd_2 (.in_1(in_3), .CLK(in_2), .out_3(regd_2_out_3));
  RegAnd regand_1 (.in_1(regd_1_out_3), .in_2(regd_2_out_3), .out_3(regand_1_out_3));
  RegNot regnot_2 (.in_1(regd_2_out_3), .out_2(regnot_2_out_2));
  RegOR regor_1 (.in_1(regd_1_out_3), .in_2(regd_2_out_3), .out_3(regor_1_out_3));
  RegXOR regxor_1 (.in_1(regd_1_out_3), .in_2(regd_2_out_3), .out_3(regxor_1_out_3));
  RegXnor regxnor_1 (.in_1(regd_1_out_3), .in_2(regd_2_out_3), .out_3(regxnor_1_out_3));
  Multiplexer #(.select(4), .width(2)) multiplexer_1 (
    .in5(comparador_1_out_5), .in6(comparador_1_out_4), .in7(comparador_1_out_3), .in8(regnor_1_out_3),
    .in9(regnand_1_out_3), .in10(regxor_1_out_3), .in11(regxnor_1_out_3), .in12(regor_1_out_3),
    .in13(regand_1_out_3), .in14(regnot_2_out_2), .in15(regnot_1_out_2), .out(out_5), .sel(in_4));  // open: in0, in1, in2, in3, in4
  RegNand regnand_1 (.in_1(regd_1_out_3), .in_2(regd_2_out_3), .out_3(regnand_1_out_3));
  comparador comparador_1 (
    .in_1(regd_1_out_3), .in_2(regd_2_out_3), .out_3(comparador_1_out_3), .out_4(comparador_1_out_4),
    .out_5(comparador_1_out_5));
  RegNor regnor_1 (.in_1(regd_1_out_3), .in_2(regd_2_out_3), .out_3(regnor_1_out_3));

  // Notes on the sheet:
  //   1111-not a    
  //   1110-not b    
  //   1101-and ab
  //   1100-or ab
  //   1011-xnor ab
  //   1010-xor ab      
  //   1001-nand ab 
  //   1000-nor ab   
  //                  0111-comparador<=>
  //   Pedro Siqueira - 405830
endmodule

module comparador (
  input  [1:0] in_1,
  input  [1:0] in_2,
  output [1:0] out_3,
  output [1:0] out_4,
  output [1:0] out_5
);

  Comparator #(.width(2), .mode("twosComplement")) comparator_1 (
    .a(in_2), .b(in_1), .gt(out_3[0]), .eq(out_4[0]), .lt(out_5[0]));
endmodule

module RegXOR (
  input  [1:0] in_1,
  input  [1:0] in_2,
  output [1:0] out_3
);

  xor xor_1 (out_3[1], in_1[1], in_1[0]);
  xor xor_2 (out_3[0], in_2[1], in_2[0]);
endmodule

module RegNand (
  input  [1:0] in_1,
  input  [1:0] in_2,
  output [1:0] out_3
);

  nand nand_1 (out_3[1], in_1[1], in_1[0]);
  nand nand_2 (out_3[0], in_2[1], in_2[0]);
endmodule

module RegNor (
  input  [1:0] in_1,
  input  [1:0] in_2,
  output [1:0] out_3
);

  nor nor_1 (out_3[1], in_1[1], in_1[0]);
  nor nor_2 (out_3[0], in_2[1], in_2[0]);
endmodule
