// Logisim project implementacao01.circ as structural Verilog: 3 circuits, main circuit main
module main (
  input  [3:0] Dado_1,
  input  [3:0] Dado_2,
  input  [2:0] in_3,
  output [3:0] AND,
  output [3:0] NOT,
  output [3:0] OR,
  output [3:0] XOR
);

  wire clock_1_out;

  Clock #(.highDuration(1), .lowDuration(1)) clock_1 (.out(clock_1_out));
  registrador registrador_1 (
    .Dado_1(Dado_1), .Dado_2(Dado_2), .Clock(clock_1_out), .Preset(in_3[2]), .Enable(in_3[1]),
    .Clear(in_3[0]), .AND(AND), .NOT1(NOT), .OR(OR), .XOR(XOR));

  // Notes on the sheet:
  //   Arquitetura de Computadores - Guia 13
  //   Implementar LU usando flip-flops do tipo D
  //   Tiago Menegaz de Melo Garcia           405844
endmodule

module registrador (
  input  Clock,
  input  [3:0] Dado_1,
  input  [3:0] Dado_2,
  input  Preset,
  input  Enable,
  input  Clear,
  output [3:0] AND,
  output [3:0] NOT1,
  output [3:0] OR,
  output [3:0] XOR
);

  wire [3:0] and_1_out, flipflopdx4_2_out_6, or_1_out, xor_1_out;

  assign and_1_out = Dado_1 & Dado_2;  // AND_Gate and_1, 4 bits wide
  assign or_1_out = Dado_1 | Dado_2;  // OR_Gate or_1, 4 bits wide
  assign xor_1_out = Dado_1 ^ Dado_2;  // XOR_Gate xor_1, 4 bits wide
  flipflopDx4 flipflopdx4_1 (
    .Clock(Clock), .in_2(and_1_out), .Preset(Preset), .Enable(Enable), .Clear(Clear), .out_6(AND));
  flipflopDx4 flipflopdx4_2 (
    .Clock(Clock), .in_2(Dado_1), .Preset(Preset), .Enable(Enable), .Clear(Clear), .out_6(flipflopdx4_2_out_6));
  assign NOT1 = ~flipflopdx4_2_out_6;  // NOT_Gate not_1, 4 bits wide
  flipflopDx4 flipflopdx4_3 (
    .Clock(Clock), .in_2(or_1_out), .Preset(Preset), .Enable(Enable), .Clear(Clear), .out_6(OR));
  flipflopDx4 flipflopdx4_4 (
    .Clock(Clock), .in_2(xor_1_out), .Preset(Preset), .Enable(Enable), .Clear(Clear), .out_6(XOR));
endmodule

module flipflopDx4 (
  input  Clock,
  input  [3:0] in_2,
  input  Preset,
  input  Enable,
  input  Clear,
  output [3:0] out_6
);

  D_Flip_Flop #(.trigger("rising")) d_ff_1 (
    .clk(Clock), .D(in_2[0]), .Q(out_6[0]), .preset(Preset), .en(Enable), .reset(Clear));  // open: Qn
  D_Flip_Flop #(.trigger("rising")) d_ff_2 (
    .clk(Clock), .D(in_2[1]), .Q(out_6[1]), .preset(Preset), .en(Enable), .reset(Clear));  // open: Qn
  D_Flip_Flop #(.trigger("rising")) d_ff_3 (
    .clk(Clock), .D(in_2[2]), .Q(out_6[2]), .preset(Preset), .en(Enable), .reset(Clear));  // open: Qn
  D_Flip_Flop #(.trigger("rising")) d_ff_4 (
    .clk(Clock), .D(in_2[3]), .Q(out_6[3]), .preset(Preset), .en(Enable), .reset(Clear));  // open: Qn
endmodule
