// Logisim project implementacao03.circ as structural Verilog: 3 circuits, main circuit main
module main (
  input  in_1,
  input  [3:0] Dado_1,
  input  [3:0] Dado_2,
  input  [2:0] in_4,
  output [3:0] AND,
  output [3:0] NOT,
  output [3:0] OR,
  output [3:0] XOR,
  output [3:0] NAND,
  output [3:0] NOR,
  output [3:0] XNOR,
  output Maior,
  output Igual,
  output Menor
);

  wire clock_1_out;

  Clock #(.highDuration(1), .lowDuration(1)) clock_1 (.out(clock_1_out));
  registrador registrador_1 (
    .Dado_1(Dado_1), .Dado_2(Dado_2), .Clock(clock_1_out), .Preset(in_4[2]), .Enable(in_4[1]),
    .Clear(in_4[0]), .AND(AND), .NOT1(NOT), .OR(OR), .XOR(XOR), .NAND(NAND), .NOR(NOR), .XNOR(XNOR),
    .Maior(Maior), .Igual(Igual), .Menor(Menor));

  // Notes on the sheet:
  //   Arquitetura de Computadores - Guia 13
  //   Implementar LU usando flip-flops do tipo D
  //   Tiago Menegaz de Melo Garcia           405844
endmodule

module registrador (
  input  Clock,
  input  [3:0] Dado_1,
  input  [3:0] Dado_2,
  input  Preset,
  input  Enable,
  input  Clear,
  output [3:0] AND,
  output [3:0] NOT1,
  output [3:0] OR,
  output [3:0] XOR,
  output [3:0] NAND,
  output [3:0] NOR,
  output [3:0] XNOR,
  output Maior,
  output Igual,
  output Menor
);

  wire [3:0] and_1_out, flipflopdx4_2_out_6, nand_1_out, nor_1_out, or_1_out, xnor_1_out, xor_1_out;

  assign and_1_out = Dado_1 & Dado_2;  // AND_Gate and_1, 4 bits wide
  assign or_1_out = Dado_1 | Dado_2;  // OR_Gate or_1, 4 bits wide
  assign xor_1_out = Dado_1 ^ Dado_2;  // XOR_Gate xor_1, 4 bits wide
  assign nand_1_out = ~(Dado_1 & Dado_2);  // NAND_Gate nand_1, 4 bits wide
  assign nor_1_out = ~(Dado_1 | Dado_2);  // NOR_Gate nor_1, 4 bits wide
  assign xnor_1_out = ~(Dado_1 ^ Dado_2);  // XNOR_Gate xnor_1, 4 bits wide
  flipflopDx4 flipflopdx4_1 (
    .Clock(Clock), .Dado(and_1_out), .Preset(Preset), .Enable(Enable), .Clear(Clear), .out_6(AND));
  flipflopDx4 flipflopdx4_2 (
    .Clock(Clock), .Dado(Dado_1), .Preset(Preset), .Enable(Enable), .Clear(Clear), .out_6(flipflopdx4_2_out_6));
  assign NOT1 = ~flipflopdx4_2_out_6;  // NOT_Gate not_1, 4 bits wide
  flipflopDx4 flipflopdx4_3 (
    .Clock(Clock), .Dado(or_1_out), .Preset(Preset), .Enable(Enable), .Clear(Clear), .out_6(OR));
  flipflopDx4 flipflopdx4_4 (
    .Clock(Clock), .Dado(xor_1_out), .Preset(Preset), .Enable(Enable), .Clear(Clear), .out_6(XOR));
  flipflopDx4 flipflopdx4_5 (
    .Clock(Clock), .Dado(nand_1_out), .Preset(Preset), .Enable(Enable), .Clear(Clear), .out_6(NAND));
  flipflopDx4 flipflopdx4_6 (
    .Clock(Clock), .Dado(nor_1_out), .Preset(Preset), .Enable(Enable), .Clear(Clear), .out_6(NOR));
  flipflopDx4 flipflopdx4_7 (
    .Clock(Clock), .Dado(xnor_1_out), .Preset(Preset), .Enable(Enable), .Clear(Clear), .out_6(XNOR));
  Comparator #(.width(4), .mode("twosComplement")) comparator_1 (
    .a(Dado_1), .b(Dado_2), .gt(Maior), .eq(Igual), .lt(Menor));
endmodule

module flipflopDx4 (
  input  Clock,
  input  [3:0] Dado,
  input  Preset,
  input  Enable,
  input  Clear,
  output [3:0] out_6
);

  D_Flip_Flop #(.trigger("rising")) d_ff_1 (
    .clk(Clock), .D(Dado[0]), .Q(out_6[0]), .preset(Preset), .en(Enable), .reset(Clear));  // open: Qn
  D_Flip_Flop #(.trigger("rising")) d_ff_2 (
    .clk(Clock), .D(Dado[1]), .Q(out_6[1]), .preset(Preset), .en(Enable), .reset(Clear));  // open: Qn
  D_Flip_Flop #(.trigger("rising")) d_ff_3 (
    .clk(Clock), .D(Dado[2]), .Q(out_6[2]), .preset(Preset), .en(Enable), .reset(Clear));  // open: Qn
  D_Flip_Flop #(.trigger("rising")) d_ff_4 (
    .clk(Clock), .D(Dado[3]), .Q(out_6[3]), .preset(Preset), .en(Enable), .reset(Clear));  // open: Qn
endmodule
