// Logisim project guia 13.circ as structural Verilog: 5 circuits, main circuit exercicio 01
module exercicio_01 (
  input  enable,
  input  clear,
  input  clock,
  input  [1:0] a1a0,
  input  [1:0] b1b0,
  output [1:0] \and ,
  output [1:0] \or ,
  output [1:0] \xor ,
  output [1:0] not_a,
  output [1:0] not_b
);

  wire and_1_out, and_2_out, not_1_out, not_2_out, not_3_out, not_4_out, or_1_out, or_2_out, xor_1_out,
       xor_2_out;

  not not_1 (not_1_out, a1a0[0]);
  not not_2 (not_2_out, a1a0[1]);
  not not_3 (not_3_out, b1b0[0]);
  not not_4 (not_4_out, b1b0[1]);
  and and_1 (and_1_out, b1b0[0], a1a0[0]);
  and and_2 (and_2_out, b1b0[1], a1a0[1]);
  or or_1 (or_1_out, b1b0[0], a1a0[0]);
  or or_2 (or_2_out, b1b0[1], a1a0[1]);
  xor xor_1 (xor_1_out, a1a0[0], b1b0[0]);
  xor xor_2 (xor_2_out, b1b0[1], a1a0[1]);
  D_Flip_Flop #(.trigger("rising")) d_ff_1 (
    .clk(clock), .D(and_1_out), .Q(\and [0]), .en(enable), .reset(clear));  // open: Qn, preset
  D_Flip_Flop #(.trigger("rising")) d_ff_2 (
    .clk(clock), .D(and_2_out), .Q(\and [1]), .en(enable), .reset(clear));  // open: Qn, preset
  D_Flip_Flop #(.trigger("rising")) d_ff_3 (
    .clk(clock), .D(or_1_out), .Q(\or [0]), .en(enable), .reset(clear));  // open: Qn, preset
  D_Flip_Flop #(.trigger("rising")) d_ff_4 (
    .clk(clock), .D(or_2_out), .Q(\or [1]), .en(enable), .reset(clear));  // open: Qn, preset
  D_Flip_Flop #(.trigger("rising")) d_ff_5 (
    .clk(clock), .D(xor_1_out), .Q(\xor [0]), .en(enable), .reset(clear));  // open: Qn, preset
  D_Flip_Flop #(.trigger("rising")) d_ff_6 (
    .clk(clock), .D(xor_2_out), .Q(\xor [1]), .en(enable), .reset(clear));  // open: Qn, preset
  D_Flip_Flop #(.trigger("rising")) d_ff_7 (
    .clk(clock), .D(not_1_out), .Q(not_a[0]), .en(enable), .reset(clear));  // open: Qn, preset
  D_Flip_Flop #(.trigger("rising")) d_ff_8 (
    .clk(clock), .D(not_2_out), .Q(not_a[1]), .en(enable), .reset(clear));  // open: Qn, preset
  D_Flip_Flop #(.trigger("rising")) d_ff_9 (
    .clk(clock), .D(not_3_out), .Q(not_b[0]), .en(enable), .reset(clear));  // open: Qn, preset
  D_Flip_Flop #(.trigger("rising")) d_ff_10 (
    .clk(clock), .D(not_4_out), .Q(not_b[1]), .en(enable), .reset(clear));  // open: Qn, preset
endmodule

module exercicio_02 (
  input  enable,
  input  clear,
  input  clock,
  input  [1:0] a1a0,
  input  [1:0] b1b0,
  output [1:0] NAND,
  output [1:0] NOR,
  output [1:0] XNOR
);

  wire nand_1_out, nand_2_out, nor_1_out, nor_2_out, xnor_1_out, xnor_2_out;

  nand nand_1 (nand_1_out, b1b0[0], a1a0[0]);
  nand nand_2 (nand_2_out, b1b0[1], a1a0[1]);
  nor nor_1 (nor_1_out, b1b0[0], a1a0[0]);
  nor nor_2 (nor_2_out, b1b0[1], a1a0[1]);
  xnor xnor_1 (xnor_1_out, a1a0[0], b1b0[0]);
  xnor xnor_2 (xnor_2_out, b1b0[1], a1a0[1]);
  D_Flip_Flop #(.trigger("rising")) d_ff_1 (
    .clk(clock), .D(nand_1_out), .Q(NAND[0]), .en(enable), .reset(clear));  // open: Qn, preset
  D_Flip_Flop #(.trigger("rising")) d_ff_2 (
    .clk(clock), .D(nand_2_out), .Q(NAND[1]), .en(enable), .reset(clear));  // open: Qn, preset
  D_Flip_Flop #(.trigger("rising")) d_ff_3 (
    .clk(clock), .D(nor_1_out), .Q(NOR[0]), .en(enable), .reset(clear));  // open: Qn, preset
  D_Flip_Flop #(.trigger("rising")) d_ff_4 (
    .clk(clock), .D(nor_2_out), .Q(NOR[1]), .en(enable), .reset(clear));  // open: Qn, preset
  D_Flip_Flop #(.trigger("rising")) d_ff_5 (
    .clk(clock), .D(xnor_1_out), .Q(XNOR[0]), .en(enable), .reset(clear));  // open: Qn, preset
  D_Flip_Flop #(.trigger("rising")) d_ff_6 (
    .clk(clock), .D(xnor_2_out), .Q(XNOR[1]), .en(enable), .reset(clear));  // open: Qn, preset
endmodule

module exercicio_03 (
  input  enable,
  input  clear,
  input  clock,
  input  [1:0] a1a0,
  input  [1:0] b1b0,
  output menor,
  output igual,
  output maior
);

  wire and_1_out, and_2_out, and_3_out, and_4_out, and_5_out, and_6_out, and_7_out, and_8_out, and_9_out,
       and_10_out, not_1_out, not_2_out, not_3_out, not_4_out, not_5_out, not_6_out, or_1_out, or_2_out,
       or_3_out;

  not not_1 (not_1_out, b1b0[0]);
  not not_2 (not_2_out, b1b0[1]);
  not not_3 (not_3_out, a1a0[0]);
  not not_4 (not_4_out, a1a0[1]);
  not not_5 (not_5_out, b1b0[0]);
  not not_6 (not_6_out, b1b0[1]);
  and and_1 (and_1_out, a1a0[0], a1a0[1], not_1_out);
  and and_2 (and_2_out, not_2_out, a1a0[1]);
  and and_3 (and_3_out, not_1_out, not_2_out, a1a0[0]);
  and and_4 (and_4_out, not_3_out, not_4_out, b1b0[0]);
  and and_5 (and_5_out, b1b0[1], not_4_out);
  and and_6 (and_6_out, b1b0[0], b1b0[1], not_3_out);
  and and_7 (and_7_out, not_6_out, not_5_out, not_3_out, not_4_out);
  and and_8 (and_8_out, b1b0[0], not_6_out, a1a0[0], not_4_out);
  and and_9 (and_9_out, not_3_out, not_5_out, b1b0[1], a1a0[1]);
  and and_10 (and_10_out, b1b0[1], b1b0[0], a1a0[0], a1a0[1]);
  or or_1 (or_1_out, and_1_out, and_2_out, and_3_out);
  or or_2 (or_2_out, and_4_out, and_5_out, and_6_out);
  or or_3 (or_3_out, and_7_out, and_8_out, and_9_out, and_10_out);
  D_Flip_Flop #(.trigger("rising")) d_ff_1 (
    .clk(clock), .D(or_2_out), .Q(menor), .en(enable), .reset(clear));  // open: Qn, preset
  D_Flip_Flop #(.trigger("rising")) d_ff_2 (
    .clk(clock), .D(or_3_out), .Q(igual), .en(enable), .reset(clear));  // open: Qn, preset
  D_Flip_Flop #(.trigger("rising")) d_ff_3 (
    .clk(clock), .D(or_1_out), .Q(maior), .en(enable), .reset(clear));  // open: Qn, preset
endmodule

module exercicio_04 (
  input  enable,
  input  clear,
  input  clock,
  input  [3:0] a3a2a1a0,
  input  [3:0] b3b2b1b0,
  output [3:0] \and ,
  output [3:0] \or ,
  output [3:0] \xor ,
  output [3:0] \nand ,
  output [3:0] \nor ,
  output [3:0] \xnor 
);

  wire and_1_out, and_2_out, and_3_out, and_4_out, nand_1_out, nand_2_out, nand_3_out, nand_4_out, nor_1_out,
       nor_2_out, nor_3_out, nor_4_out, nor_5_out, nor_6_out, nor_7_out, nor_8_out, or_1_out, or_2_out,
       or_3_out, or_4_out, xor_1_out, xor_2_out, xor_3_out, xor_4_out;

  nor nor_1 (nor_1_out, a3a2a1a0[0], b3b2b1b0[0]);
  nor nor_2 (nor_2_out, a3a2a1a0[1], b3b2b1b0[1]);
  nor nor_3 (nor_3_out, a3a2a1a0[2], b3b2b1b0[2]);
  nor nor_4 (nor_4_out, b3b2b1b0[3], a3a2a1a0[3]);
  nor nor_5 (nor_5_out, a3a2a1a0[0], b3b2b1b0[0]);
  nor nor_6 (nor_6_out, a3a2a1a0[1], b3b2b1b0[1]);
  nor nor_7 (nor_7_out, a3a2a1a0[2], b3b2b1b0[2]);
  nor nor_8 (nor_8_out, b3b2b1b0[3], a3a2a1a0[3]);
  and and_1 (and_1_out, a3a2a1a0[0], b3b2b1b0[0]);
  and and_2 (and_2_out, a3a2a1a0[1], b3b2b1b0[1]);
  and and_3 (and_3_out, a3a2a1a0[2], b3b2b1b0[2]);
  and and_4 (and_4_out, b3b2b1b0[3], a3a2a1a0[3]);
  or or_1 (or_1_out, a3a2a1a0[0], b3b2b1b0[0]);
  or or_2 (or_2_out, a3a2a1a0[1], b3b2b1b0[1]);
  or or_3 (or_3_out, a3a2a1a0[2], b3b2b1b0[2]);
  or or_4 (or_4_out, b3b2b1b0[3], a3a2a1a0[3]);
  xor xor_1 (xor_1_out, a3a2a1a0[0], b3b2b1b0[0]);
  xor xor_2 (xor_2_out, a3a2a1a0[1], b3b2b1b0[1]);
  xor xor_3 (xor_3_out, a3a2a1a0[2], b3b2b1b0[2]);
  xor xor_4 (xor_4_out, b3b2b1b0[3], a3a2a1a0[3]);
  nand nand_1 (nand_1_out, a3a2a1a0[0], b3b2b1b0[0]);
  nand nand_2 (nand_2_out, a3a2a1a0[1], b3b2b1b0[1]);
  nand nand_3 (nand_3_out, a3a2a1a0[2], b3b2b1b0[2]);
  nand nand_4 (nand_4_out, b3b2b1b0[3], a3a2a1a0[3]);
  D_Flip_Flop #(.trigger("rising")) d_ff_1 (
    .clk(clear), .D(and_1_out), .Q(\and [0]), .en(clear), .reset(clear));  // open: Qn, preset
  D_Flip_Flop #(.trigger("rising")) d_ff_2 (
    .clk(clear), .D(and_2_out), .Q(\and [1]), .en(clear), .reset(clear));  // open: Qn, preset
  D_Flip_Flop #(.trigger("rising")) d_ff_3 (
    .clk(clear), .D(and_3_out), .Q(\and [2]), .preset(clear), .en(clear), .reset(clear));  // open: Qn
  D_Flip_Flop #(.trigger("rising")) d_ff_4 (
    .clk(clear), .D(and_4_out), .Q(\and [3]), .en(clear), .reset(clear));  // open: Qn, preset
  D_Flip_Flop #(.trigger("rising")) d_ff_5 (
    .clk(clear), .D(or_1_out), .Q(\or [0]), .en(clear), .reset(clear));  // open: Qn, preset
  D_Flip_Flop #(.trigger("rising")) d_ff_6 (
    .clk(clear), .D(or_2_out), .Q(\or [1]), .en(clear), .reset(clear));  // open: Qn, preset
  D_Flip_Flop #(.trigger("rising")) d_ff_7 (
    .clk(clear), .D(or_3_out), .Q(\or [2]), .en(clear), .reset(clear));  // open: Qn, preset
  D_Flip_Flop #(.trigger("rising")) d_ff_8 (
    .clk(clear), .D(or_4_out), .Q(\or [3]), .en(clear), .reset(clear));  // open: Qn, preset
  D_Flip_Flop #(.trigger("rising")) d_ff_9 (
    .clk(clear), .D(xor_1_out), .Q(\xor [0]), .en(clear), .reset(clear));  // open: Qn, preset
  D_Flip_Flop #(.trigger("rising")) d_ff_10 (
    .clk(clear), .D(xor_2_out), .Q(\xor [1]), .en(clear), .reset(clear));  // open: Qn, preset
  D_Flip_Flop #(.trigger("rising")) d_ff_11 (
    .clk(clear), .D(xor_3_out), .Q(\xor [2]), .en(clear), .reset(clear));  // open: Qn, preset
  D_Flip_Flop #(.trigger("rising")) d_ff_12 (
    .clk(clear), .D(xor_4_out), .Q(\xor [3]), .en(clear), .reset(clear));  // open: Qn, preset
  D_Flip_Flop #(.trigger("rising")) d_ff_13 (
    .clk(clear), .D(nand_1_out), .Q(\nand [0]), .en(clear), .reset(clear));  // open: Qn, preset
  D_Flip_Flop #(.trigger("rising")) d_ff_14 (
    .clk(clear), .D(nand_2_out), .Q(\nand [1]), .en(clear), .reset(clear));  // open: Qn, preset
  D_Flip_Flop #(.trigger("rising")) d_ff_15 (
    .clk(clear), .D(nand_3_out), .Q(\nand [2]), .en(clear), .reset(clear));  // open: Qn, preset
  D_Flip_Flop #(.trigger("rising")) d_ff_16 (
    .clk(clear), .D(nand_4_out), .Q(\nand [3]), .en(clear), .reset(clear));  // open: Qn, preset
  D_Flip_Flop #(.trigger("rising")) d_ff_17 (
    .clk(clear), .D(nor_1_out), .Q(\nor [0]), .en(clear), .reset(clear));  // open: Qn, preset
  D_Flip_Flop #(.trigger("rising")) d_ff_18 (
    .clk(clear), .D(nor_2_out), .Q(\nor [1]), .en(clear), .reset(clear));  // open: Qn, preset
  D_Flip_Flop #(.trigger("rising")) d_ff_19 (
    .clk(clear), .D(nor_3_out), .Q(\nor [2]), .en(clear), .reset(clear));  // open: Qn, preset
  D_Flip_Flop #(.trigger("rising")) d_ff_20 (
    .clk(clear), .D(nor_4_out), .Q(\nor [3]), .en(clear), .reset(clear));  // open: Qn, preset
  D_Flip_Flop #(.trigger("rising")) d_ff_21 (
    .clk(clear), .D(nor_5_out), .Q(\xnor [0]), .en(clear), .reset(clear));  // open: Qn, preset
  D_Flip_Flop #(.trigger("rising")) d_ff_22 (
    .clk(clear), .D(nor_6_out), .Q(\xnor [1]), .en(clear), .reset(clear));  // open: Qn, preset
  D_Flip_Flop #(.trigger("rising")) d_ff_23 (
    .clk(clear), .D(nor_7_out), .Q(\xnor [2]), .en(clear), .reset(clear));  // open: Qn, preset
  D_Flip_Flop #(.trigger("rising")) d_ff_24 (
    .clk(clear), .D(nor_8_out), .Q(\xnor [3]), .en(clear), .reset(clear));  // open: Qn, preset

  assign clock = clear;
  assign enable = clear;
endmodule

module main (
  input  [1:0] A,
  input  [1:0] B,
  input  enable,
  input  clear,
  input  [1:0] A_2,
  input  [1:0] B_2,
  input  enable_2,
  input  clear_2,
  input  [1:0] A_3,
  input  [1:0] B_3,
  input  enable_3,
  input  clear_3,
  input  [3:0] A_4,
  input  [3:0] B_4,
  input  enable_4,
  input  clear_4,
  output [1:0] \and ,
  output [1:0] \or ,
  output [1:0] \xor ,
  output [1:0] not_a,
  output [1:0] not_b,
  output [1:0] \nand ,
  output [1:0] \nor ,
  output [1:0] \xnor ,
  output menor,
  output igual,
  output maior,
  output [3:0] and_2,
  output [3:0] or_2,
  output [3:0] xor_2,
  output [3:0] nand_2,
  output [3:0] nor_2,
  output [3:0] xnor_2
);

  wire clock_1_out, clock_2_out, clock_3_out, clock_4_out;

  exercicio_01 exercicio_01_1 (
    .a1a0(A), .b1b0(B), .enable(enable), .clear(clear), .clock(clock_1_out), .\and (\and ), .\or (\or ),
    .\xor (\xor ), .not_a(not_a), .not_b(not_b));
  exercicio_02 exercicio_02_1 (
    .a1a0(A_2), .b1b0(B_2), .enable(enable_2), .clear(clear_2), .clock(clock_2_out), .NAND(\nand ),
    .NOR(\nor ), .XNOR(\xnor ));
  exercicio_03 exercicio_03_1 (
    .a1a0(A_3), .b1b0(B_3), .enable(enable_3), .clear(clear_3), .clock(clock_3_out), .menor(menor),
    .igual(igual), .maior(maior));
  exercicio_04 exercicio_04_1 (
    .a3a2a1a0(A_4), .b3b2b1b0(B_4), .enable(enable_4), .clear(clear_4), .clock(clock_4_out), .\and (and_2),
    .\or (or_2), .\xor (xor_2), .\nand (nand_2), .\nor (nor_2), .\xnor (xnor_2));
  Clock #(.highDuration(1), .lowDuration(1)) clock_1 (.out(clock_1_out));
  Clock #(.highDuration(1), .lowDuration(1)) clock_2 (.out(clock_2_out));
  Clock #(.highDuration(1), .lowDuration(1)) clock_3 (.out(clock_3_out));
  Clock #(.highDuration(1), .lowDuration(1)) clock_4 (.out(clock_4_out));
endmodule
