// Logisim project Guia13.circ as structural Verilog: 7 circuits, main circuit main
module main (
  input  [1:0] A,
  input  Enable,
  input  Clear,
  input  [1:0] B,
  output [1:0] AND,
  output [1:0] Not_A,
  output [1:0] OR,
  output [1:0] XOR,
  output [1:0] NAND,
  output [1:0] NOR,
  output [1:0] XNOR,
  output Menor,
  output Igual,
  output Maior
);

  wire Clock_out;

  Clock #(.highDuration(1), .lowDuration(1)) Clock (.out(Clock_out));
  Exercicio03 exercicio03_1 (
    .a(A), .b(B), .En(Enable), .Clr(Clear), .Clk(Clock_out), .AND(AND), .Not_A(Not_A), .OR(OR), .XOR(XOR),
    .NAND(NAND), .NOR(NOR), .XNOR(XNOR), .Menor(Menor), .Igual(Igual), .Maior(Maior));
endmodule

module Exercicio01 (
  input  En,
  input  Clr,
  input  Clk,
  input  [1:0] a,
  input  [1:0] b,
  output [1:0] AND,
  output [1:0] Not_A,
  output [1:0] OR,
  output [1:0] XOR,
  output [1:0] a_Out,
  output [1:0] b_Out,
  output En_Out,
  output Clr_Out,
  output Clk_Out
);

  wire [1:0] and_1_out, or_1_out, xor_1_out;

  assign and_1_out = a & b;  // AND_Gate and_1, 2 bits wide
  assign or_1_out = a | b;  // OR_Gate or_1, 2 bits wide
  assign xor_1_out = a ^ b;  // XOR_Gate xor_1, 2 bits wide
  D_Flip_Flop #(.trigger("rising")) d_ff_1 (
    .clk(Clk), .D(and_1_out[0]), .Q(AND[0]), .en(En), .reset(Clr));  // open: Qn, preset
  D_Flip_Flop #(.trigger("rising")) d_ff_2 (
    .clk(Clk), .D(and_1_out[1]), .Q(AND[1]), .en(En), .reset(Clr));  // open: Qn, preset
  D_Flip_Flop #(.trigger("rising")) d_ff_3 (
    .clk(Clk), .D(a[0]), .Qn(Not_A[0]), .en(En), .reset(Clr));  // open: Q, preset
  D_Flip_Flop #(.trigger("rising")) d_ff_4 (
    .clk(Clk), .D(a[1]), .Qn(Not_A[1]), .en(En), .reset(Clr));  // open: Q, preset
  D_Flip_Flop #(.trigger("rising")) d_ff_5 (
    .clk(Clk), .D(or_1_out[0]), .Q(OR[0]), .en(En), .reset(Clr));  // open: Qn, preset
  D_Flip_Flop #(.trigger("rising")) d_ff_6 (
    .clk(Clk), .D(or_1_out[1]), .Q(OR[1]), .en(En), .reset(Clr));  // open: Qn, preset
  D_Flip_Flop #(.trigger("rising")) d_ff_7 (
    .clk(Clk), .D(xor_1_out[0]), .Q(XOR[0]), .en(En), .reset(Clr));  // open: Qn, preset
  D_Flip_Flop #(.trigger("rising")) d_ff_8 (
    .clk(Clk), .D(xor_1_out[1]), .Q(XOR[1]), .en(En), .reset(Clr));  // open: Qn, preset

  assign a_Out = a;
  assign b_Out = b;
  assign Clk_Out = Clk;
  assign Clr_Out = Clr;
  assign En_Out = En;
endmodule

module Exercicio02 (
  input  [1:0] a,
  input  [1:0] b,
  input  En,
  input  Clr,
  input  Clk,
  output [1:0] AND,
  output [1:0] Not_A,
  output [1:0] OR,
  output [1:0] XOR,
  output [1:0] NAND,
  output [1:0] NOR,
  output [1:0] XNOR,
  output [1:0] a_Out,
  output [1:0] b_Out,
  output En_Out,
  output Clr_Out,
  output Clk_Out
);

  wire [1:0] nand_1_out, nor_1_out, xnor_1_out;

  assign nand_1_out = ~(a_Out & b_Out);  // NAND_Gate nand_1, 2 bits wide
  assign nor_1_out = ~(a_Out | b_Out);  // NOR_Gate nor_1, 2 bits wide
  assign xnor_1_out = ~(a_Out ^ b_Out);  // XNOR_Gate xnor_1, 2 bits wide
  Exercicio01 exercicio01_1 (
    .a(a), .b(b), .En(En), .Clr(Clr), .Clk(Clk), .a_Out(a_Out), .b_Out(b_Out), .En_Out(En_Out),
    .Clr_Out(Clr_Out), .Clk_Out(Clk_Out), .AND(AND), .Not_A(Not_A), .OR(OR), .XOR(XOR));
  D_Flip_Flop #(.trigger("rising")) d_ff_1 (
    .clk(Clk_Out), .D(nand_1_out[0]), .Q(NAND[0]), .en(En_Out), .reset(Clr_Out));  // open: Qn, preset
  D_Flip_Flop #(.trigger("rising")) d_ff_2 (
    .clk(Clk_Out), .D(nand_1_out[1]), .Q(NAND[1]), .en(En_Out), .reset(Clr_Out));  // open: Qn, preset
  D_Flip_Flop #(.trigger("rising")) d_ff_3 (
    .clk(Clk_Out), .D(nor_1_out[0]), .Q(NOR[0]), .en(En_Out), .reset(Clr_Out));  // open: Qn, preset
  D_Flip_Flop #(.trigger("rising")) d_ff_4 (
    .clk(Clk_Out), .D(nor_1_out[1]), .Q(NOR[1]), .en(En_Out), .reset(Clr_Out));  // open: Qn, preset
  D_Flip_Flop #(.trigger("rising")) d_ff_5 (
    .clk(Clk_Out), .D(xnor_1_out[0]), .Q(XNOR[0]), .en(En_Out), .reset(Clr_Out));  // open: Qn, preset
  D_Flip_Flop #(.trigger("rising")) d_ff_6 (
    .clk(Clk_Out), .D(xnor_1_out[1]), .Q(XNOR[1]), .en(En_Out), .reset(Clr_Out));  // open: Qn, preset
endmodule

module Exercicio03 (
  input  [1:0] a,
  input  [1:0] b,
  input  En,
  input  Clr,
  input  Clk,
  output [1:0] AND,
  output [1:0] Not_A,
  output [1:0] OR,
  output [1:0] XOR,
  output [1:0] NAND,
  output [1:0] NOR,
  output [1:0] XNOR,
  output Menor,
  output Igual,
  output Maior
);

  wire equal_1_equal, exercicio02_1_clk_out, exercicio02_1_clr_out, exercicio02_1_en_out,
       greater_than_1_a___b, less_than_1_a___b;
  wire [1:0] exercicio02_1_a_out, exercicio02_1_b_out;

  Less_than less_than_1 (.a(exercicio02_1_a_out), .b(exercicio02_1_b_out), .A___B(less_than_1_a___b));
  Equal equal_1 (.a(exercicio02_1_a_out), .b(exercicio02_1_b_out), .equal(equal_1_equal));
  Greater_than greater_than_1 (.a(exercicio02_1_a_out), .b(exercicio02_1_b_out), .A___B(greater_than_1_a___b));
  Exercicio02 exercicio02_1 (
    .a(a), .b(b), .En(En), .Clr(Clr), .Clk(Clk), .a_Out(exercicio02_1_a_out), .b_Out(exercicio02_1_b_out),
    .En_Out(exercicio02_1_en_out), .Clr_Out(exercicio02_1_clr_out), .Clk_Out(exercicio02_1_clk_out),
    .AND(AND), .Not_A(Not_A), .OR(OR), .XOR(XOR), .NAND(NAND), .NOR(NOR), .XNOR(XNOR));
  D_Flip_Flop #(.trigger("rising")) d_ff_1 (
    .clk(exercicio02_1_clk_out), .D(less_than_1_a___b), .Q(Menor), .en(exercicio02_1_en_out),
    .reset(exercicio02_1_clr_out));  // open: Qn, preset
  D_Flip_Flop #(.trigger("rising")) d_ff_2 (
    .clk(exercicio02_1_clk_out), .D(equal_1_equal), .Q(Igual), .en(exercicio02_1_en_out),
    .reset(exercicio02_1_clr_out));  // open: Qn, preset
  D_Flip_Flop #(.trigger("rising")) d_ff_3 (
    .clk(exercicio02_1_clk_out), .D(greater_than_1_a___b), .Q(Maior), .en(exercicio02_1_en_out),
    .reset(exercicio02_1_clr_out));  // open: Qn, preset
endmodule

module Equal (
  input  [1:0] a,
  input  [1:0] b,
  output equal
);

  wire xor_1_out, xor_2_out;

  xor xor_1 (xor_1_out, a[0], b[0]);
  xor xor_2 (xor_2_out, a[1], b[1]);
  nor nor_1 (equal, xor_1_out, xor_2_out);
endmodule

module Greater_than (
  input  [1:0] a,
  input  [1:0] b,
  output A___B
);

  wire and_1_out, and_2_out, and_3_out;
  wire [1:0] not_1_out, not_2_out;

  assign not_1_out = ~a;  // NOT_Gate not_1, 2 bits wide
  assign not_2_out = ~b;  // NOT_Gate not_2, 2 bits wide
  and and_1 (and_1_out, a[1], not_2_out[1]);
  and and_2 (and_2_out, a[1], a[0], not_2_out[0]);
  and and_3 (and_3_out, a[0], not_2_out[0], not_2_out[1]);
  or or_1 (A___B, and_1_out, and_2_out, and_3_out);
endmodule

module Less_than (
  input  [1:0] a,
  input  [1:0] b,
  output A___B
);

  wire and_1_out, and_2_out, and_3_out;
  wire [1:0] not_1_out, not_2_out;

  assign not_1_out = ~a;  // NOT_Gate not_1, 2 bits wide
  assign not_2_out = ~b;  // NOT_Gate not_2, 2 bits wide
  and and_1 (and_1_out, not_1_out[1], b[1]);
  and and_2 (and_2_out, not_1_out[1], not_1_out[0], b[0]);
  and and_3 (and_3_out, not_1_out[0], b[1], b[0]);
  or or_1 (A___B, and_1_out, and_2_out, and_3_out);
endmodule
