// Logisim project 412727.circ as structural Verilog: 23 circuits, main circuit main
module main (
);


  // Notes on the sheet:
  //   AUGUSTO FERREIRA ANDRADE DO CARMO - 412727 - GUIA 13
endmodule

module reg_2bits (
  input  clk,
  input  Ad,
  input  Ald,
  input  Aen,
  input  Bd,
  input  Bld,
  input  Ben,
  output [1:0] out_8
);

  wire d_ff_1_q, d_ff_2_q;

  assign out_8[0] = Ald ? d_ff_1_q : 1'bz;  // Controlled_Buffer controlled_buffer_1
  D_Flip_Flop #(.trigger("rising")) d_ff_1 (.clk(clk), .D(Ad), .Q(d_ff_1_q), .en(Aen));  // open: Qn, preset, reset
  assign out_8[1] = Bld ? d_ff_2_q : 1'bz;  // Controlled_Buffer controlled_buffer_2
  D_Flip_Flop #(.trigger("rising")) d_ff_2 (.clk(clk), .D(Bd), .Q(d_ff_2_q), .en(Ben));  // open: Qn, preset, reset
endmodule

module xor_2bits (
  input  [1:0] in_1,
  input  [1:0] in_2,
  output [1:0] out_3
);

  assign out_3 = in_1 ^ in_2;  // XOR_Gate xor_1, 2 bits wide
endmodule

module or_2bits (
  input  [1:0] in_1,
  input  [1:0] in_2,
  output [1:0] out_3
);

  assign out_3 = in_1 | in_2;  // OR_Gate or_1, 2 bits wide
endmodule

module and_2bits (
  input  [1:0] in_1,
  input  [1:0] in_2,
  output [1:0] out_3
);

  assign out_3 = in_1 & in_2;  // AND_Gate and_1, 2 bits wide
endmodule

module not_2bits (
  input  [1:0] in_1,
  output [1:0] out_2
);

  assign out_2 = ~in_1;  // NOT_Gate not_1, 2 bits wide
endmodule

module \Exercício_1  (
  input  clk,
  input  [1:0] A,
  input  [1:0] A0en_ld,
  input  [1:0] A1en_ld,
  input  [1:0] B,
  input  [1:0] B0en_ld,
  input  [1:0] B1en_ld,
  input  [2:0] in_8,
  output [1:0] out_9
);

  wire [1:0] and_2bits_1_out_3, not_2bits_1_out_2, not_2bits_2_out_2, or_2bits_1_out_3, reg_2bits_1_out_8,
       reg_2bits_2_out_8, xor_2bits_1_out_3;

  reg_2bits reg_2bits_1 (
    .Ad(A[0]), .Ald(A0en_ld[0]), .Aen(A0en_ld[1]), .Bd(A[1]), .Bld(A1en_ld[0]), .Ben(A1en_ld[1]), .clk(clk),
    .out_8(reg_2bits_1_out_8));
  reg_2bits reg_2bits_2 (
    .Ad(B[0]), .Ald(B0en_ld[0]), .Aen(B0en_ld[1]), .Bd(B[1]), .Bld(B1en_ld[0]), .Ben(B1en_ld[1]), .clk(clk),
    .out_8(reg_2bits_2_out_8));
  xor_2bits xor_2bits_1 (.in_1(reg_2bits_1_out_8), .in_2(reg_2bits_2_out_8), .out_3(xor_2bits_1_out_3));
  or_2bits or_2bits_1 (.in_1(reg_2bits_1_out_8), .in_2(reg_2bits_2_out_8), .out_3(or_2bits_1_out_3));
  and_2bits and_2bits_1 (.in_1(reg_2bits_1_out_8), .in_2(reg_2bits_2_out_8), .out_3(and_2bits_1_out_3));
  not_2bits not_2bits_1 (.in_1(reg_2bits_1_out_8), .out_2(not_2bits_1_out_2));
  not_2bits not_2bits_2 (.in_1(reg_2bits_2_out_8), .out_2(not_2bits_2_out_2));
  Multiplexer #(.select(3), .width(2)) multiplexer_1 (
    .in0(xor_2bits_1_out_3), .in1(or_2bits_1_out_3), .in2(and_2bits_1_out_3), .in3(not_2bits_1_out_2),
    .in4(not_2bits_2_out_2), .out(out_9), .sel(in_8));  // open: in5, in6, in7

  // Notes on the sheet:
  //   xor
  //   or
  //   and
  //   not_A
  //   not_B
  //   000
  //   001
  //   010
  //   011
  //   100
endmodule

module nand_2bits (
  input  [1:0] in_1,
  input  [1:0] in_2,
  output [1:0] out_3
);

  assign out_3 = ~(in_1 & in_2);  // NAND_Gate nand_1, 2 bits wide
endmodule

module nor_2bits (
  input  [1:0] in_1,
  input  [1:0] in_2,
  output [1:0] out_3
);

  assign out_3 = ~(in_1 | in_2);  // NOR_Gate nor_1, 2 bits wide
endmodule

module xnor_2bits (
  input  [1:0] in_1,
  input  [1:0] in_2,
  output [1:0] out_3
);

  assign out_3 = ~(in_1 ^ in_2);  // XNOR_Gate xnor_1, 2 bits wide
endmodule

module Exercicio_2 (
  input  clk,
  input  [1:0] A,
  input  [1:0] A0en_ld,
  input  [1:0] A1en_ld,
  input  [1:0] B,
  input  [1:0] B0en_ld,
  input  [1:0] B1en_ld,
  input  [2:0] in_8,
  output [1:0] out_9
);

  wire [1:0] and_2bits_1_out_3, nand_2bits_1_out_3, nor_2bits_1_out_3, not_2bits_1_out_2, not_2bits_2_out_2,
       or_2bits_1_out_3, reg_2bits_1_out_8, reg_2bits_2_out_8, xnor_2bits_1_out_3, xor_2bits_1_out_3;

  reg_2bits reg_2bits_1 (
    .Ad(A[0]), .Ald(A0en_ld[0]), .Aen(A0en_ld[1]), .Bd(A[1]), .Bld(A1en_ld[0]), .Ben(A1en_ld[1]), .clk(clk),
    .out_8(reg_2bits_1_out_8));
  reg_2bits reg_2bits_2 (
    .Ad(B[0]), .Ald(B0en_ld[0]), .Aen(B0en_ld[1]), .Bd(B[1]), .Bld(B1en_ld[0]), .Ben(B1en_ld[1]), .clk(clk),
    .out_8(reg_2bits_2_out_8));
  xor_2bits xor_2bits_1 (.in_1(reg_2bits_1_out_8), .in_2(reg_2bits_2_out_8), .out_3(xor_2bits_1_out_3));
  or_2bits or_2bits_1 (.in_1(reg_2bits_1_out_8), .in_2(reg_2bits_2_out_8), .out_3(or_2bits_1_out_3));
  and_2bits and_2bits_1 (.in_1(reg_2bits_1_out_8), .in_2(reg_2bits_2_out_8), .out_3(and_2bits_1_out_3));
  not_2bits not_2bits_1 (.in_1(reg_2bits_1_out_8), .out_2(not_2bits_1_out_2));
  not_2bits not_2bits_2 (.in_1(reg_2bits_2_out_8), .out_2(not_2bits_2_out_2));
  nand_2bits nand_2bits_1 (.in_1(reg_2bits_1_out_8), .in_2(reg_2bits_2_out_8), .out_3(nand_2bits_1_out_3));
  nor_2bits nor_2bits_1 (.in_1(reg_2bits_1_out_8), .in_2(reg_2bits_2_out_8), .out_3(nor_2bits_1_out_3));
  xnor_2bits xnor_2bits_1 (.in_1(reg_2bits_1_out_8), .in_2(reg_2bits_2_out_8), .out_3(xnor_2bits_1_out_3));
  Multiplexer #(.select(3), .width(2)) multiplexer_1 (
    .in0(xor_2bits_1_out_3), .in1(or_2bits_1_out_3), .in2(and_2bits_1_out_3), .in3(not_2bits_1_out_2),
    .in4(not_2bits_2_out_2), .in5(nand_2bits_1_out_3), .in6(nor_2bits_1_out_3), .in7(xnor_2bits_1_out_3),
    .out(out_9), .sel(in_8));

  // Notes on the sheet:
  //   xor
  //   000
  //   or
  //   001
  //   and
  //   010
  //   not_A
  //   011
  //   not_B
  //   100
  //   nand
  //   101
  //   nor
  //   110
  //   xnor
  //   111
endmodule

module comparador_2bits (
  input  [1:0] in_1,
  input  [1:0] in_2,
  output out_3,
  output out_4,
  output out_5
);

  Comparator #(.width(2), .mode("twosComplement")) comparator_1 (
    .a(in_1), .b(in_2), .gt(out_3), .eq(out_4), .lt(out_5));
endmodule

module \Exercício_3  (
  input  in_1,
  input  [1:0] A,
  input  [1:0] A0en_ld,
  input  [1:0] A1en_ld,
  input  [1:0] B,
  input  [1:0] B0en_ld,
  input  [1:0] B1en_ld,
  input  [3:0] in_8,
  output [1:0] out_9
);

  wire [0:0] comparador_2bits_1_out_3, comparador_2bits_1_out_4, comparador_2bits_1_out_5;
  wire [1:0] and_2bits_1_out_3, nand_2bits_1_out_3, nor_2bits_1_out_3, not_2bits_1_out_2, not_2bits_2_out_2,
       or_2bits_1_out_3, reg_2bits_1_out_8, reg_2bits_2_out_8, xnor_2bits_1_out_3, xor_2bits_1_out_3;

  reg_2bits reg_2bits_1 (
    .Ad(A[0]), .Ald(A0en_ld[0]), .Aen(A0en_ld[1]), .Bd(A[1]), .Bld(A1en_ld[0]), .Ben(A1en_ld[1]), .clk(in_1),
    .out_8(reg_2bits_1_out_8));
  reg_2bits reg_2bits_2 (
    .Ad(B[0]), .Ald(B0en_ld[0]), .Aen(B0en_ld[1]), .Bd(B[1]), .Bld(B1en_ld[0]), .Ben(B1en_ld[1]), .clk(in_1),
    .out_8(reg_2bits_2_out_8));
  // Probe on reg_2bits_2_out_8
  // Probe on reg_2bits_1_out_8
  // Probe on xor_2bits_1_out_3
  xor_2bits xor_2bits_1 (.in_1(reg_2bits_1_out_8), .in_2(reg_2bits_2_out_8), .out_3(xor_2bits_1_out_3));
  or_2bits or_2bits_1 (.in_1(reg_2bits_1_out_8), .in_2(reg_2bits_2_out_8), .out_3(or_2bits_1_out_3));
  and_2bits and_2bits_1 (.in_1(reg_2bits_1_out_8), .in_2(reg_2bits_2_out_8), .out_3(and_2bits_1_out_3));
  not_2bits not_2bits_1 (.in_1(reg_2bits_1_out_8), .out_2(not_2bits_1_out_2));
  not_2bits not_2bits_2 (.in_1(reg_2bits_2_out_8), .out_2(not_2bits_2_out_2));
  nand_2bits nand_2bits_1 (.in_1(reg_2bits_1_out_8), .in_2(reg_2bits_2_out_8), .out_3(nand_2bits_1_out_3));
  nor_2bits nor_2bits_1 (.in_1(reg_2bits_1_out_8), .in_2(reg_2bits_2_out_8), .out_3(nor_2bits_1_out_3));
  xnor_2bits xnor_2bits_1 (.in_1(reg_2bits_1_out_8), .in_2(reg_2bits_2_out_8), .out_3(xnor_2bits_1_out_3));
  comparador_2bits comparador_2bits_1 (
    .in_1(reg_2bits_1_out_8), .in_2(reg_2bits_2_out_8), .out_3(comparador_2bits_1_out_3[0]),
    .out_4(comparador_2bits_1_out_4[0]), .out_5(comparador_2bits_1_out_5[0]));
  Multiplexer #(.select(4), .width(2)) multiplexer_1 (
    .in0(xor_2bits_1_out_3), .in1(or_2bits_1_out_3), .in2(and_2bits_1_out_3), .in3(not_2bits_1_out_2),
    .in4(not_2bits_2_out_2), .in5(nand_2bits_1_out_3), .in6(nor_2bits_1_out_3), .in7(xnor_2bits_1_out_3),
    .in8({1'b0, comparador_2bits_1_out_3[0]}), .in9({1'b0, comparador_2bits_1_out_4[0]}),
    .in10({1'b0, comparador_2bits_1_out_5[0]}), .sel(in_8));  // open: in11, in12, in13, in14, in15, out

  // Notes on the sheet:
  //   xor
  //   000
  //   or
  //   001
  //   and
  //   010
  //   not_A
  //   011
  //   not_B
  //   100
  //   nand
  //   101
  //   nor
  //   110
  //   xnor
  //   111
  //   (>)1000
  //   (=)1001
  //   (<)1010
  //   obs: o output está aparecendo
  //   como indefenido nesse exercicio
  //   mas não consegui descobrir o por que
endmodule

module reg_4bits (
  input  clk,
  input  Ad,
  input  Ald,
  input  Aen,
  input  Bd,
  input  Bld,
  input  Ben,
  input  Cd,
  input  Cld,
  input  Cen,
  input  Dd,
  input  Dld,
  input  Den,
  output [3:0] out_14
);

  wire d_ff_1_q, d_ff_2_q, d_ff_3_q, d_ff_4_q;

  assign out_14[0] = Ald ? d_ff_1_q : 1'bz;  // Controlled_Buffer controlled_buffer_1
  D_Flip_Flop #(.trigger("rising")) d_ff_1 (.clk(clk), .D(Ad), .Q(d_ff_1_q), .en(Aen));  // open: Qn, preset, reset
  D_Flip_Flop #(.trigger("rising")) d_ff_2 (.clk(clk), .D(Bd), .Q(d_ff_2_q), .en(Ben));  // open: Qn, preset, reset
  assign out_14[1] = Bld ? d_ff_2_q : 1'bz;  // Controlled_Buffer controlled_buffer_2
  assign out_14[2] = Cld ? d_ff_3_q : 1'bz;  // Controlled_Buffer controlled_buffer_3
  D_Flip_Flop #(.trigger("rising")) d_ff_3 (.clk(clk), .D(Cd), .Q(d_ff_3_q), .en(Cen));  // open: Qn, preset, reset
  D_Flip_Flop #(.trigger("rising")) d_ff_4 (.clk(clk), .D(Dd), .Q(d_ff_4_q), .en(Den));  // open: Qn, preset, reset
  assign out_14[3] = Dld ? d_ff_4_q : 1'bz;  // Controlled_Buffer controlled_buffer_4
endmodule

module \Exercícios_4_5  (
  input  clk,
  input  [3:0] A,
  input  [7:0] Aen_ld,
  input  [3:0] B,
  input  [7:0] Ben_ld,
  input  [3:0] in_6,
  output [3:0] out_7
);

  wire [3:0] and_4bits_1_out_3, nand_4bits_1_out_3, nor_4bits_1_out_3, not_4bits_1_out_2, not_4bits_2_out_2,
       or_4bits_1_out_3, reg_4bits_1_out_14, reg_4bits_2_out_14, xnor_4bits_1_out_3, xor_4bits_1_out_3;

  reg_4bits reg_4bits_1 (
    .Ad(A[0]), .Ald(Aen_ld[0]), .Aen(Aen_ld[1]), .Bd(A[1]), .Bld(Aen_ld[2]), .Ben(Aen_ld[3]), .Cd(A[2]),
    .Cld(Aen_ld[4]), .Cen(Aen_ld[5]), .Dd(A[3]), .Dld(Aen_ld[6]), .Den(Aen_ld[7]), .clk(clk),
    .out_14(reg_4bits_1_out_14));
  reg_4bits reg_4bits_2 (
    .Ad(B[0]), .Ald(Ben_ld[0]), .Aen(Ben_ld[1]), .Bd(B[1]), .Bld(Ben_ld[2]), .Ben(Ben_ld[3]), .Cd(B[2]),
    .Cld(Ben_ld[4]), .Cen(Ben_ld[5]), .Dd(B[3]), .Dld(Ben_ld[6]), .Den(Ben_ld[7]), .clk(clk),
    .out_14(reg_4bits_2_out_14));
  // Probe on reg_4bits_2_out_14
  // Probe on reg_4bits_1_out_14
  // Probe on xor_4bits_1_out_3
  xor_4bits xor_4bits_1 (.in_1(reg_4bits_1_out_14), .in_2(reg_4bits_2_out_14), .out_3(xor_4bits_1_out_3));
  or_4bits or_4bits_1 (.in_1(reg_4bits_1_out_14), .in_2(reg_4bits_2_out_14), .out_3(or_4bits_1_out_3));
  and_4bits and_4bits_1 (.in_1(reg_4bits_1_out_14), .in_2(reg_4bits_2_out_14), .out_3(and_4bits_1_out_3));
  not_4bits not_4bits_1 (.in_1(reg_4bits_1_out_14), .out_2(not_4bits_1_out_2));
  not_4bits not_4bits_2 (.in_1(reg_4bits_2_out_14), .out_2(not_4bits_2_out_2));
  nand_4bits nand_4bits_1 (.in_1(reg_4bits_1_out_14), .in_2(reg_4bits_2_out_14), .out_3(nand_4bits_1_out_3));
  nor_4bits nor_4bits_1 (.in_1(reg_4bits_1_out_14), .in_2(reg_4bits_2_out_14), .out_3(nor_4bits_1_out_3));
  xnor_4bits xnor_4bits_1 (.in_1(reg_4bits_1_out_14), .in_2(reg_4bits_2_out_14), .out_3(xnor_4bits_1_out_3));
  Multiplexer #(.select(4), .width(4)) multiplexer_1 (
    .in0(xor_4bits_1_out_3), .in1(or_4bits_1_out_3), .in2(and_4bits_1_out_3), .in3(not_4bits_1_out_2),
    .in4(not_4bits_2_out_2), .in5(nand_4bits_1_out_3), .in6(nor_4bits_1_out_3), .in7(xnor_4bits_1_out_3),
    .sel(in_6));  // open: in8, in9, in10, in11, in12, in13, in14, in15, out

  // Notes on the sheet:
  //   000
  //   001
  //   010
  //   011
  //   100
  //   101
  //   110
  //   111
  //   obs: o output está aparecendo
  //   como indefenido nesse exercicio
  //   mas não consegui descobrir o por que
  //   or
  //   and
  //   not_A
  //   not_B
  //   nand
  //   nor
  //   xnor
endmodule

module xor_4bits (
  input  [3:0] in_1,
  input  [3:0] in_2,
  output [3:0] out_3
);

  assign out_3 = in_1 ^ in_2;  // XOR_Gate xor_1, 4 bits wide
endmodule

module or_4bits (
  input  [3:0] in_1,
  input  [3:0] in_2,
  output [3:0] out_3
);

  assign out_3 = in_1 | in_2;  // OR_Gate or_1, 4 bits wide
endmodule

module and_4bits (
  input  [3:0] in_1,
  input  [3:0] in_2,
  output [3:0] out_3
);

  assign out_3 = in_1 & in_2;  // AND_Gate and_1, 4 bits wide
endmodule

module not_4bits (
  input  [3:0] in_1,
  output [3:0] out_2
);

  assign out_2 = ~in_1;  // NOT_Gate not_1, 4 bits wide
endmodule

module nand_4bits (
  input  [3:0] in_1,
  input  [3:0] in_2,
  output [3:0] out_3
);

  assign out_3 = ~(in_1 & in_2);  // NAND_Gate nand_1, 4 bits wide
endmodule

module nor_4bits (
  input  [3:0] in_1,
  input  [3:0] in_2,
  output [3:0] out_3
);

  assign out_3 = ~(in_1 | in_2);  // NOR_Gate nor_1, 4 bits wide
endmodule

module xnor_4bits (
  input  [3:0] in_1,
  input  [3:0] in_2,
  output [3:0] out_3
);

  assign out_3 = ~(in_1 ^ in_2);  // XNOR_Gate xnor_1, 4 bits wide
endmodule

module comparador_4bits (
  input  [3:0] in_1,
  input  [3:0] in_2,
  output out_3,
  output out_4,
  output out_5
);

  Comparator #(.width(4), .mode("twosComplement")) comparator_1 (
    .a(in_1), .b(in_2), .gt(out_3), .eq(out_4), .lt(out_5));
endmodule
