// Logisim project Guia13.circ as structural Verilog
module Ex01 (
  input  [1:0] a,
  input  [1:0] b,
  input  Clear,
  input  [1:0] op,
  output [1:0] s
);

  wire clock_out;
  wire [1:0] and_1_out, d_ff_3_q, d_ff_4_q, not_1_out, or_1_out, xor_1_out;

  Clock #(.highDuration(1), .lowDuration(1)) clock (.out(clock_out));
  D_Flip_Flop #(.trigger("rising")) d_ff_1 (
    .clk(clock_out), .D(a[1]), .Q(d_ff_3_q[1]), .reset(Clear));  // open: Qn, preset, en
  D_Flip_Flop #(.trigger("rising")) d_ff_2 (
    .clk(clock_out), .D(b[1]), .Q(d_ff_4_q[1]), .reset(Clear));  // open: Qn, preset, en
  D_Flip_Flop #(.trigger("rising")) d_ff_3 (
    .clk(clock_out), .D(a[0]), .Q(d_ff_3_q[0]), .reset(Clear));  // open: Qn, preset, en
  D_Flip_Flop #(.trigger("rising")) d_ff_4 (
    .clk(clock_out), .D(b[0]), .Q(d_ff_4_q[0]), .reset(Clear));  // open: Qn, preset, en
  assign and_1_out = d_ff_3_q & d_ff_4_q;  // AND_Gate and_1, 2 bits wide
  assign or_1_out = d_ff_3_q | d_ff_4_q;  // OR_Gate or_1, 2 bits wide
  assign xor_1_out = d_ff_3_q ^ d_ff_4_q;  // XOR_Gate xor_1, 2 bits wide
  assign not_1_out = ~d_ff_3_q;  // NOT_Gate not_1, 2 bits wide
  Multiplexer #(.select(2), .width(2)) multiplexer_1 (
    .in0(not_1_out), .in1(and_1_out), .in2(or_1_out), .in3(xor_1_out), .out(s), .sel(op));

  // Notes on the sheet:
  //   Operacoes
  //   00 - Not (A)
  //   01 - And (A.B)
  //   10 - Or (A+B)
  //   11 - Xor (A^B)
endmodule

module Ex02 (
  input  [1:0] a,
  input  [1:0] b,
  input  Clear,
  input  [1:0] op,
  output [1:0] s
);

  wire clock_out;
  wire [1:0] d_ff_3_q, d_ff_4_q, nand_1_out, nor_1_out, xnor_1_out;

  Clock #(.highDuration(1), .lowDuration(1)) clock (.out(clock_out));
  D_Flip_Flop #(.trigger("rising")) d_ff_1 (
    .clk(clock_out), .D(a[1]), .Q(d_ff_3_q[1]), .reset(Clear));  // open: Qn, preset, en
  D_Flip_Flop #(.trigger("rising")) d_ff_2 (
    .clk(clock_out), .D(b[1]), .Q(d_ff_4_q[1]), .reset(Clear));  // open: Qn, preset, en
  D_Flip_Flop #(.trigger("rising")) d_ff_3 (
    .clk(clock_out), .D(a[0]), .Q(d_ff_3_q[0]), .reset(Clear));  // open: Qn, preset, en
  D_Flip_Flop #(.trigger("rising")) d_ff_4 (
    .clk(clock_out), .D(b[0]), .Q(d_ff_4_q[0]), .reset(Clear));  // open: Qn, preset, en
  assign nand_1_out = ~(d_ff_3_q & d_ff_4_q);  // NAND_Gate nand_1, 2 bits wide
  assign nor_1_out = ~(d_ff_3_q | d_ff_4_q);  // NOR_Gate nor_1, 2 bits wide
  assign xnor_1_out = ~(d_ff_3_q ^ d_ff_4_q);  // XNOR_Gate xnor_1, 2 bits wide
  Multiplexer #(.select(2), .width(2)) multiplexer_1 (
    .in0(d_ff_3_q), .in1(nand_1_out), .in2(nor_1_out), .in3(xnor_1_out), .out(s), .sel(op));

  // Notes on the sheet:
  //   Operacoes
  //   00 - (A)
  //   10 - Nor (A+B)'
  //   01 - Nand (A.B)'
  //   11 - Xnor (A^B)'
endmodule

module Ex03 (
  input  [1:0] a,
  input  [1:0] b,
  input  Clear,
  output A___B,
  output A___B_2,
  output A___B_3
);

  wire and_1_out, and_2_out, and_3_out, Clock_out, d_ff_1_q, d_ff_1_qn, d_ff_2_q, d_ff_3_q, d_ff_3_qn,
       d_ff_4_q, not_1_out, not_2_out, xnor_1_out, xnor_2_out;

  Clock #(.highDuration(1), .lowDuration(1)) Clock (.out(Clock_out));
  D_Flip_Flop #(.trigger("rising")) d_ff_1 (
    .clk(Clock_out), .D(a[1]), .Q(d_ff_1_q), .Qn(d_ff_1_qn), .reset(Clear));  // open: preset, en
  D_Flip_Flop #(.trigger("rising")) d_ff_2 (
    .clk(Clock_out), .D(b[1]), .Q(d_ff_2_q), .reset(Clear));  // open: Qn, preset, en
  D_Flip_Flop #(.trigger("rising")) d_ff_3 (
    .clk(Clock_out), .D(a[0]), .Q(d_ff_3_q), .Qn(d_ff_3_qn), .reset(Clear));  // open: preset, en
  D_Flip_Flop #(.trigger("rising")) d_ff_4 (
    .clk(Clock_out), .D(b[0]), .Q(d_ff_4_q), .reset(Clear));  // open: Qn, preset, en
  and and_1 (and_1_out, d_ff_1_qn, d_ff_3_qn, d_ff_4_q);
  and and_2 (and_2_out, d_ff_3_q, d_ff_1_qn, d_ff_2_q);
  xnor xnor_1 (xnor_1_out, d_ff_3_q, d_ff_4_q);
  xnor xnor_2 (xnor_2_out, d_ff_1_q, d_ff_2_q);
  and and_3 (and_3_out, d_ff_4_q, d_ff_3_qn, d_ff_1_qn, d_ff_2_q);
  not not_1 (not_1_out, A___B_2);
  and and_4 (A___B_2, xnor_1_out, xnor_2_out);
  or or_1 (A___B, and_1_out, and_3_out, and_2_out);
  not not_2 (not_2_out, A___B);
  and and_5 (A___B_3, not_2_out, not_1_out);

  // Notes on the sheet:
  //   A< B = ~a1~a0b0 + ~a1~a0b1~b0 + ~a1a0b1 
endmodule

module Ex04 (
  input  [3:0] a,
  input  [3:0] b,
  input  Clear,
  input  [1:0] op,
  output [3:0] s
);

  wire clock_out;
  wire [3:0] and_1_out, d_ff_7_q, d_ff_8_q, not_1_out, or_1_out, xor_1_out;

  Clock #(.highDuration(1), .lowDuration(1)) clock (.out(clock_out));
  D_Flip_Flop #(.trigger("rising")) d_ff_1 (
    .clk(clock_out), .D(a[3]), .Q(d_ff_7_q[3]), .reset(Clear));  // open: Qn, preset, en
  D_Flip_Flop #(.trigger("rising")) d_ff_2 (
    .clk(clock_out), .D(b[3]), .Q(d_ff_8_q[3]), .reset(Clear));  // open: Qn, preset, en
  D_Flip_Flop #(.trigger("rising")) d_ff_3 (
    .clk(clock_out), .D(a[2]), .Q(d_ff_7_q[2]), .reset(Clear));  // open: Qn, preset, en
  D_Flip_Flop #(.trigger("rising")) d_ff_4 (
    .clk(clock_out), .D(b[2]), .Q(d_ff_8_q[2]), .reset(Clear));  // open: Qn, preset, en
  D_Flip_Flop #(.trigger("rising")) d_ff_5 (
    .clk(clock_out), .D(a[1]), .Q(d_ff_7_q[1]), .reset(Clear));  // open: Qn, preset, en
  D_Flip_Flop #(.trigger("rising")) d_ff_6 (
    .clk(clock_out), .D(b[1]), .Q(d_ff_8_q[1]), .reset(Clear));  // open: Qn, preset, en
  D_Flip_Flop #(.trigger("rising")) d_ff_7 (
    .clk(clock_out), .D(a[0]), .Q(d_ff_7_q[0]), .reset(Clear));  // open: Qn, preset, en
  D_Flip_Flop #(.trigger("rising")) d_ff_8 (
    .clk(clock_out), .D(b[0]), .Q(d_ff_8_q[0]), .reset(Clear));  // open: Qn, preset, en
  assign and_1_out = d_ff_7_q & d_ff_8_q;  // AND_Gate and_1, 4 bits wide
  assign or_1_out = d_ff_7_q | d_ff_8_q;  // OR_Gate or_1, 4 bits wide
  assign xor_1_out = d_ff_7_q ^ d_ff_8_q;  // XOR_Gate xor_1, 4 bits wide
  assign not_1_out = ~d_ff_7_q;  // NOT_Gate not_1, 4 bits wide
  Multiplexer #(.select(2), .width(4)) multiplexer_1 (
    .in0(not_1_out), .in1(and_1_out), .in2(or_1_out), .in3(xor_1_out), .out(s), .sel(op));

  // Notes on the sheet:
  //   Operacoes
  //   00 - Not (A)
  //   01 - And (A.B)
  //   10 - Or (A+B)
  //   11 - Xor (A^B)
endmodule

module Ex04_b (
  input  [3:0] a,
  input  [3:0] b,
  input  Clear,
  input  [1:0] op,
  output [3:0] s
);

  wire clock_out;
  wire [3:0] d_ff_7_q, d_ff_8_q, nand_1_out, nor_1_out, xnor_1_out;

  Clock #(.highDuration(1), .lowDuration(1)) clock (.out(clock_out));
  D_Flip_Flop #(.trigger("rising")) d_ff_1 (
    .clk(clock_out), .D(a[3]), .Q(d_ff_7_q[3]), .reset(Clear));  // open: Qn, preset, en
  D_Flip_Flop #(.trigger("rising")) d_ff_2 (
    .clk(clock_out), .D(b[3]), .Q(d_ff_8_q[3]), .reset(Clear));  // open: Qn, preset, en
  D_Flip_Flop #(.trigger("rising")) d_ff_3 (
    .clk(clock_out), .D(a[2]), .Q(d_ff_7_q[2]), .reset(Clear));  // open: Qn, preset, en
  D_Flip_Flop #(.trigger("rising")) d_ff_4 (
    .clk(clock_out), .D(b[2]), .Q(d_ff_8_q[2]), .reset(Clear));  // open: Qn, preset, en
  D_Flip_Flop #(.trigger("rising")) d_ff_5 (
    .clk(clock_out), .D(a[1]), .Q(d_ff_7_q[1]), .reset(Clear));  // open: Qn, preset, en
  D_Flip_Flop #(.trigger("rising")) d_ff_6 (
    .clk(clock_out), .D(b[1]), .Q(d_ff_8_q[1]), .reset(Clear));  // open: Qn, preset, en
  D_Flip_Flop #(.trigger("rising")) d_ff_7 (
    .clk(clock_out), .D(a[0]), .Q(d_ff_7_q[0]), .reset(Clear));  // open: Qn, preset, en
  D_Flip_Flop #(.trigger("rising")) d_ff_8 (
    .clk(clock_out), .D(b[0]), .Q(d_ff_8_q[0]), .reset(Clear));  // open: Qn, preset, en
  assign nand_1_out = ~(d_ff_7_q & d_ff_8_q);  // NAND_Gate nand_1, 4 bits wide
  assign nor_1_out = ~(d_ff_7_q | d_ff_8_q);  // NOR_Gate nor_1, 4 bits wide
  assign xnor_1_out = ~(d_ff_7_q ^ d_ff_8_q);  // XNOR_Gate xnor_1, 4 bits wide
  Multiplexer #(.select(2), .width(4)) multiplexer_1 (
    .in0(d_ff_7_q), .in1(nand_1_out), .in2(nor_1_out), .in3(xnor_1_out), .out(s), .sel(op));

  // Notes on the sheet:
  //   Operacoes
  //   00 - (A)
  //   01 - Nand (A.B)'
  //   10 - Nor (A+B)'
  //   11 - Xnor (A^B)'
endmodule
