// Logisim project 04_e_05.circ as structural Verilog
module REGISTRADOR (
  input  in_1,
  input  [3:0] in_2,
  output [3:0] out_3
);

  D_Flip_Flop #(.trigger("rising")) d_ff_1 (.clk(in_1), .D(in_2[0]), .Q(out_3[0]));  // open: Qn, preset, en, reset
  D_Flip_Flop #(.trigger("rising")) d_ff_2 (.clk(in_1), .D(in_2[1]), .Q(out_3[1]));  // open: Qn, preset, en, reset
  D_Flip_Flop #(.trigger("rising")) d_ff_3 (.clk(in_1), .D(in_2[2]), .Q(out_3[2]));  // open: Qn, preset, en, reset
  D_Flip_Flop #(.trigger("rising")) d_ff_4 (.clk(in_1), .D(in_2[3]), .Q(out_3[3]));  // open: Qn, preset, en, reset

  // Notes on the sheet:
  //   Felipe Augusto
  //   415517
endmodule

module LU (
  input  [3:0] A,
  input  [3:0] B,
  output Maior,
  output Igual,
  output Menor,
  output [3:0] NOT_A,
  output [3:0] NOT_B,
  output [3:0] out_8,
  output [3:0] out_9,
  output [3:0] out_10,
  output [3:0] out_11,
  output [3:0] out_12,
  output [3:0] out_13
);

  wire clock_1_out;
  wire [3:0] registrador_1_out_3, registrador_2_out_3;

  Clock #(.highDuration(1), .lowDuration(1)) clock_1 (.out(clock_1_out));
  REGISTRADOR registrador_1 (.in_1(clock_1_out), .in_2(A), .out_3(registrador_1_out_3));
  REGISTRADOR registrador_2 (.in_1(clock_1_out), .in_2(B), .out_3(registrador_2_out_3));
  Comparator #(.width(4), .mode("twosComplement")) comparator_1 (
    .a(registrador_1_out_3), .b(registrador_2_out_3), .gt(Maior), .eq(Igual), .lt(Menor));
  assign NOT_A = ~registrador_1_out_3;  // NOT_Gate not_1, 4 bits wide
  assign NOT_B = ~registrador_2_out_3;  // NOT_Gate not_2, 4 bits wide
  assign out_8 = registrador_1_out_3 & registrador_2_out_3;  // AND_Gate and_1, 4 bits wide
  assign out_9 = registrador_1_out_3 | registrador_2_out_3;  // OR_Gate or_1, 4 bits wide
  assign out_10 = registrador_1_out_3 ^ registrador_2_out_3;  // XOR_Gate xor_1, 4 bits wide
  assign out_11 = ~(registrador_1_out_3 & registrador_2_out_3);  // NAND_Gate nand_1, 4 bits wide
  assign out_12 = ~(registrador_1_out_3 | registrador_2_out_3);  // NOR_Gate nor_1, 4 bits wide
  assign out_13 = ~(registrador_1_out_3 ^ registrador_2_out_3);  // XNOR_Gate xnor_1, 4 bits wide

  // Notes on the sheet:
  //   Felipe Augusto
  //   415517
endmodule
