// Logisim project UL_2bits.circ as structural Verilog: 10 circuits, main circuit UL_2bits
module UL_2bits (
  input  [1:0] A,
  input  [1:0] B,
  input  [3:0] Select,
  output [1:0] out_4
);

  wire Clock_out;
  wire [1:0] and_2bits_1_out_3, comparador_2bits_1_out_3, comparador_2bits_1_out_4, comparador_2bits_1_out_5,
       nand_2bits_1_saida, nor_2bits_1_saida, not_2_bits_1_out_2, not_2_bits_2_out_2, or_2bits_1_out_3,
       reg_ul_1_saida, reg_ul_2_saida, xnor_2bits_1_saida, xor_2bits_1_saida;

  Clock #(.highDuration(1), .lowDuration(1)) Clock (.out(Clock_out));
  REG_UL reg_ul_1 (.clock(Clock_out), .Input(A), .Saida(reg_ul_1_saida));
  REG_UL reg_ul_2 (.clock(Clock_out), .Input(B), .Saida(reg_ul_2_saida));
  NOT_2_bits not_2_bits_1 (.Input(reg_ul_1_saida), .out_2(not_2_bits_1_out_2));
  NOT_2_bits not_2_bits_2 (.Input(reg_ul_2_saida), .out_2(not_2_bits_2_out_2));
  OR_2bits or_2bits_1 (.A(reg_ul_1_saida), .B(reg_ul_2_saida), .out_3(or_2bits_1_out_3));
  AND_2bits and_2bits_1 (.A(reg_ul_1_saida), .B(reg_ul_2_saida), .out_3(and_2bits_1_out_3));
  XOR_2bits xor_2bits_1 (.in_1(reg_ul_1_saida), .in_2(reg_ul_2_saida), .Saida(xor_2bits_1_saida));
  NAND_2bits nand_2bits_1 (.in_1(reg_ul_1_saida), .in_2(reg_ul_2_saida), .Saida(nand_2bits_1_saida));
  NOR_2bits nor_2bits_1 (.in_1(reg_ul_1_saida), .in_2(reg_ul_2_saida), .Saida(nor_2bits_1_saida));
  XNOR_2bits xnor_2bits_1 (.in_1(reg_ul_1_saida), .in_2(reg_ul_2_saida), .Saida(xnor_2bits_1_saida));
  Comparador_2bits comparador_2bits_1 (
    .A(reg_ul_1_saida), .B(reg_ul_2_saida), .out_3(comparador_2bits_1_out_3),
    .out_4(comparador_2bits_1_out_4), .out_5(comparador_2bits_1_out_5));
  Multiplexer #(.select(4), .width(2)) multiplexer_1 (
    .in0(not_2_bits_1_out_2), .in1(not_2_bits_2_out_2), .in2(or_2bits_1_out_3), .in3(and_2bits_1_out_3),
    .in4(xor_2bits_1_saida), .in5(nand_2bits_1_saida), .in6(nor_2bits_1_saida), .in7(xnor_2bits_1_saida),
    .in8(comparador_2bits_1_out_3), .in9(comparador_2bits_1_out_4), .in10(comparador_2bits_1_out_5),
    .out(out_4), .sel(Select));  // open: in11, in12, in13, in14, in15

  // Notes on the sheet:
  //   Unidade Lógica
  //   Jonathan Felipe Xavier    Matricula:415704
  //   Tabela de operações
  //   0000 - Not A
  //   0001 - Not B
  //   0010 - Or
  //   0011 - And
  //   0100 - Xor
  //   0101 - Nand
  //   0110 - Nor
  //   0111 - Xnor
  //   1000 - Compa >
  //   1001 - Comp =
  //   1010 - Comp <
endmodule

module REG_UL (
  input  clock,
  input  [1:0] Input,
  output [1:0] Saida
);

  D_Flip_Flop #(.trigger("rising")) d_ff_1 (.clk(clock), .D(Input[0]), .Q(Saida[0]));  // open: Qn, preset, en, reset
  D_Flip_Flop #(.trigger("rising")) d_ff_2 (.clk(clock), .D(Input[1]), .Q(Saida[1]));  // open: Qn, preset, en, reset

  // Notes on the sheet:
  //   Jonathan Felipe Xavier    Matricula:415704
endmodule

module NOT_2_bits (
  input  [1:0] Input,
  output [1:0] out_2
);

  not not_1 (out_2[0], Input[0]);
  not not_2 (out_2[1], Input[1]);

  // Notes on the sheet:
  //   Jonathan Felipe Xavier    Matricula:415704
endmodule

module OR_2bits (
  input  [1:0] A,
  input  [1:0] B,
  output [1:0] out_3
);

  or or_1 (out_3[0], A[0], B[0]);
  or or_2 (out_3[1], A[1], B[1]);

  // Notes on the sheet:
  //   Jonathan Felipe Xavier    Matricula:415704
endmodule

module AND_2bits (
  input  [1:0] A,
  input  [1:0] B,
  output [1:0] out_3
);

  and and_1 (out_3[0], A[0], B[0]);
  and and_2 (out_3[1], A[1], B[1]);

  // Notes on the sheet:
  //   Jonathan Felipe Xavier    Matricula:415704
endmodule

module XOR_2bits (
  input  [1:0] in_1,
  input  [1:0] in_2,
  output [1:0] Saida
);

  xor xor_1 (Saida[0], in_1[0], in_2[0]);
  xor xor_2 (Saida[1], in_1[1], in_2[1]);

  // Notes on the sheet:
  //   Jonathan Felipe Xavier    Matricula:415704
endmodule

module NAND_2bits (
  input  [1:0] in_1,
  input  [1:0] in_2,
  output [1:0] Saida
);

  nand nand_1 (Saida[0], in_1[0], in_2[0]);
  nand nand_2 (Saida[1], in_1[1], in_2[1]);

  // Notes on the sheet:
  //   Jonathan Felipe Xavier    Matricula:415704
endmodule

module NOR_2bits (
  input  [1:0] in_1,
  input  [1:0] in_2,
  output [1:0] Saida
);

  nor nor_1 (Saida[0], in_1[0], in_2[0]);
  nor nor_2 (Saida[1], in_1[1], in_2[1]);

  // Notes on the sheet:
  //   Jonathan Felipe Xavier    Matricula:415704
endmodule

module XNOR_2bits (
  input  [1:0] in_1,
  input  [1:0] in_2,
  output [1:0] Saida
);

  xnor xnor_1 (Saida[0], in_1[0], in_2[0]);
  xnor xnor_2 (Saida[1], in_1[1], in_2[1]);

  // Notes on the sheet:
  //   Jonathan Felipe Xavier    Matricula:415704
endmodule

module Comparador_2bits (
  input  [1:0] A,
  input  [1:0] B,
  output [1:0] out_3,
  output [1:0] out_4,
  output [1:0] out_5
);

  wire comparator_1_gt;

  Comparator #(.width(2), .mode("twosComplement")) comparator_1 (
    .a(A), .b(B), .gt(comparator_1_gt), .eq(out_3[0]), .lt(out_4[1]));

  assign out_5 = out_4;

  // Notes on the sheet:
  //   Jonathan Felipe Xavier    Matricula:415704
endmodule
