// Logisim project UL_4bits.circ as structural Verilog: 10 circuits, main circuit UL_4bits
module UL_4bits (
  input  [3:0] A,
  input  [3:0] B,
  input  [3:0] Select,
  output [3:0] out_4
);

  wire Clock_out;
  wire [3:0] and_4bits_1_out_3, comparador_4bits_1_out_3, comparador_4bits_1_out_4, comparador_4bits_1_out_5,
       nand_4bits_1_out_3, nor_4bits_1_out_3, not_4_bits_1_out_2, not_4_bits_2_out_2, or_4bits_1_out_3,
       reg_ul_1_saida, reg_ul_2_saida, xnor_4bits_1_out_3, xor_4bits_1_out_3;

  Clock #(.highDuration(1), .lowDuration(1)) Clock (.out(Clock_out));
  REG_UL reg_ul_1 (.clock(Clock_out), .Input(A), .Saida(reg_ul_1_saida));
  REG_UL reg_ul_2 (.clock(Clock_out), .Input(B), .Saida(reg_ul_2_saida));
  NOT_4_bits not_4_bits_1 (.Input(reg_ul_1_saida), .out_2(not_4_bits_1_out_2));
  NOT_4_bits not_4_bits_2 (.Input(reg_ul_2_saida), .out_2(not_4_bits_2_out_2));
  OR_4bits or_4bits_1 (.A(reg_ul_1_saida), .B(reg_ul_2_saida), .out_3(or_4bits_1_out_3));
  AND_4bits and_4bits_1 (.A(reg_ul_1_saida), .B(reg_ul_2_saida), .out_3(and_4bits_1_out_3));
  XOR_4bits xor_4bits_1 (.A(reg_ul_1_saida), .B(reg_ul_2_saida), .out_3(xor_4bits_1_out_3));
  NAND_4bits nand_4bits_1 (.A(reg_ul_1_saida), .B(reg_ul_2_saida), .out_3(nand_4bits_1_out_3));
  NOR_4bits nor_4bits_1 (.A(reg_ul_1_saida), .B(reg_ul_2_saida), .out_3(nor_4bits_1_out_3));
  XNOR_4bits xnor_4bits_1 (.A(reg_ul_1_saida), .B(reg_ul_2_saida), .out_3(xnor_4bits_1_out_3));
  Comparador_4bits comparador_4bits_1 (
    .A(reg_ul_1_saida), .B(reg_ul_2_saida), .out_3(comparador_4bits_1_out_3),
    .out_4(comparador_4bits_1_out_4), .out_5(comparador_4bits_1_out_5));
  Multiplexer #(.select(4), .width(4)) multiplexer_1 (
    .in0(not_4_bits_1_out_2), .in1(not_4_bits_2_out_2), .in2(or_4bits_1_out_3), .in3(and_4bits_1_out_3),
    .in4(xor_4bits_1_out_3), .in5(nand_4bits_1_out_3), .in6(nor_4bits_1_out_3), .in7(xnor_4bits_1_out_3),
    .in8(comparador_4bits_1_out_3), .in9(comparador_4bits_1_out_4), .in10(comparador_4bits_1_out_5),
    .out(out_4), .sel(Select));  // open: in11, in12, in13, in14, in15

  // Notes on the sheet:
  //   Unidade Lógica
  //   Jonathan Felipe Xavier    Matricula:415704
  //   Tabela de operações
  //   0000 - Not A
  //   0001 - Not B
  //   0010 - Or
  //   0011 - And
  //   0100 - Xor
  //   0101 - Nand
  //   0110 - Nor
  //   0111 - Xnor
  //   1000 - Compa >
  //   1001 - Comp =
  //   1010 - Comp <
endmodule

module REG_UL (
  input  clock,
  input  [3:0] Input,
  output [3:0] Saida
);

  D_Flip_Flop #(.trigger("rising")) d_ff_1 (.clk(clock), .D(Input[0]), .Q(Saida[0]));  // open: Qn, preset, en, reset
  D_Flip_Flop #(.trigger("rising")) d_ff_2 (.clk(clock), .D(Input[1]), .Q(Saida[1]));  // open: Qn, preset, en, reset
  D_Flip_Flop #(.trigger("rising")) d_ff_3 (.clk(clock), .D(Input[2]), .Q(Saida[2]));  // open: Qn, preset, en, reset
  D_Flip_Flop #(.trigger("rising")) d_ff_4 (.clk(clock), .D(Input[3]), .Q(Saida[3]));  // open: Qn, preset, en, reset

  // Notes on the sheet:
  //   Jonathan Felipe Xavier    Matricula:415704
endmodule

module NOT_4_bits (
  input  [3:0] Input,
  output [3:0] out_2
);

  not not_1 (out_2[0], Input[0]);
  not not_2 (out_2[1], Input[1]);
  not not_3 (out_2[2], Input[2]);
  not not_4 (out_2[3], Input[3]);

  // Notes on the sheet:
  //   Jonathan Felipe Xavier    Matricula:415704
endmodule

module OR_4bits (
  input  [3:0] A,
  input  [3:0] B,
  output [3:0] out_3
);

  or or_1 (out_3[0], A[0], B[0]);
  or or_2 (out_3[1], A[1], B[1]);
  or or_3 (out_3[2], A[2], B[2]);
  or or_4 (out_3[3], A[3], B[3]);

  // Notes on the sheet:
  //   Jonathan Felipe Xavier    Matricula:415704
endmodule

module AND_4bits (
  input  [3:0] A,
  input  [3:0] B,
  output [3:0] out_3
);

  and and_1 (out_3[0], A[0], B[0]);
  and and_2 (out_3[1], A[1], B[1]);
  and and_3 (out_3[2], A[2], B[2]);
  and and_4 (out_3[3], A[3], B[3]);

  // Notes on the sheet:
  //   Jonathan Felipe Xavier    Matricula:415704
endmodule

module XOR_4bits (
  input  [3:0] A,
  input  [3:0] B,
  output [3:0] out_3
);

  xor xor_1 (out_3[0], A[0], B[0]);
  xor xor_2 (out_3[1], A[1], B[1]);
  xor xor_3 (out_3[2], A[2], B[2]);
  xor xor_4 (out_3[3], A[3], B[3]);

  // Notes on the sheet:
  //   Jonathan Felipe Xavier    Matricula:415704
endmodule

module NAND_4bits (
  input  [3:0] A,
  input  [3:0] B,
  output [3:0] out_3
);

  nand nand_1 (out_3[0], A[0], B[0]);
  nand nand_2 (out_3[1], A[1], B[1]);
  nand nand_3 (out_3[2], A[2], B[2]);
  nand nand_4 (out_3[3], A[3], B[3]);

  // Notes on the sheet:
  //   Jonathan Felipe Xavier    Matricula:415704
endmodule

module NOR_4bits (
  input  [3:0] A,
  input  [3:0] B,
  output [3:0] out_3
);

  nor nor_1 (out_3[0], A[0], B[0]);
  nor nor_2 (out_3[1], A[1], B[1]);
  nor nor_3 (out_3[2], A[2], B[2]);
  nor nor_4 (out_3[3], A[3], B[3]);

  // Notes on the sheet:
  //   Jonathan Felipe Xavier    Matricula:415704
endmodule

module XNOR_4bits (
  input  [3:0] A,
  input  [3:0] B,
  output [3:0] out_3
);

  xnor xnor_1 (out_3[0], A[0], B[0]);
  xnor xnor_2 (out_3[1], A[1], B[1]);
  xnor xnor_3 (out_3[2], A[2], B[2]);
  xnor xnor_4 (out_3[3], A[3], B[3]);

  // Notes on the sheet:
  //   Jonathan Felipe Xavier    Matricula:415704
endmodule

module Comparador_4bits (
  input  [3:0] A,
  input  [3:0] B,
  output [3:0] out_3,
  output [3:0] out_4,
  output [3:0] out_5
);

  wire comparator_1_gt;

  Comparator #(.width(4), .mode("twosComplement")) comparator_1 (
    .a(A), .b(B), .gt(comparator_1_gt), .eq(out_3[1]), .lt(out_4[2]));

  assign out_5[1:0] = out_4[3:2];

  // Notes on the sheet:
  //   Jonathan Felipe Xavier    Matricula:415704
endmodule
