// Logisim project Exercicio01_guia13.circ as structural Verilog: 2 circuits, main circuit registrador de dois bits
module registrador_de_dois_bits (
  input  CLK,
  input  [1:0] DADOS,
  output [1:0] SAIDA
);

  D_Flip_Flop #(.trigger("rising")) d_ff_1 (.clk(CLK), .D(DADOS[1]), .Q(SAIDA[1]));  // open: Qn, preset, en, reset
  D_Flip_Flop #(.trigger("rising")) d_ff_2 (.clk(CLK), .D(DADOS[0]), .Q(SAIDA[0]));  // open: Qn, preset, en, reset

  // Notes on the sheet:
  //   Registrador 
  //   Marcos Felipe Martins Silva-415719
endmodule

module Logical_Unit (
  input  [1:0] DADO1,
  input  [1:0] DADO2,
  output [1:0] NOT1,
  output [1:0] NOT2,
  output [1:0] AND,
  output [1:0] OR,
  output [1:0] XOR
);

  wire clock_1_out;
  wire [1:0] registrador_de_dois_bits_1_saida, registrador_de_dois_bits_2_saida;

  registrador_de_dois_bits registrador_de_dois_bits_1 (
    .CLK(clock_1_out), .DADOS(DADO1), .SAIDA(registrador_de_dois_bits_1_saida));
  Clock #(.highDuration(1), .lowDuration(1)) clock_1 (.out(clock_1_out));
  registrador_de_dois_bits registrador_de_dois_bits_2 (
    .CLK(clock_1_out), .DADOS(DADO2), .SAIDA(registrador_de_dois_bits_2_saida));
  assign NOT1 = ~registrador_de_dois_bits_1_saida;  // NOT_Gate not_1, 2 bits wide
  assign NOT2 = ~registrador_de_dois_bits_2_saida;  // NOT_Gate not_2, 2 bits wide
  assign AND = registrador_de_dois_bits_1_saida & registrador_de_dois_bits_2_saida;  // AND_Gate and_1, 2 bits wide
  assign OR = registrador_de_dois_bits_1_saida | registrador_de_dois_bits_2_saida;  // OR_Gate or_1, 2 bits wide
  assign XOR = registrador_de_dois_bits_1_saida ^ registrador_de_dois_bits_2_saida;  // XOR_Gate xor_1, 2 bits wide

  // Notes on the sheet:
  //   Logical Unit
  //   Marcos Felipe Martins Silva-415719
endmodule
