// Logisim project Exercicio02_guia13.circ as structural Verilog: 2 circuits, main circuit registrador de dois bits
module registrador_de_dois_bits (
  input  CLK,
  input  [1:0] DADOS,
  output [1:0] SAIDA
);

  D_Flip_Flop #(.trigger("rising")) d_ff_1 (.clk(CLK), .D(DADOS[0]), .Q(SAIDA[1]));  // open: Qn, preset, en, reset
  D_Flip_Flop #(.trigger("rising")) d_ff_2 (.clk(CLK), .D(DADOS[1]), .Q(SAIDA[0]));  // open: Qn, preset, en, reset

  // Notes on the sheet:
  //   Registrador 
  //   Marcos Felipe Martins Silva-415719
endmodule

module Logical_Unit (
  input  [1:0] DADOS1,
  input  in_2,
  input  [1:0] DADOS2,
  output [1:0] NAND,
  output [1:0] NOR,
  output [1:0] XNOR
);

  wire [1:0] registrador_de_dois_bits_1_saida, registrador_de_dois_bits_2_saida, undriven;

  registrador_de_dois_bits registrador_de_dois_bits_1 (
    .CLK(in_2), .DADOS(DADOS1), .SAIDA(registrador_de_dois_bits_1_saida));
  registrador_de_dois_bits registrador_de_dois_bits_2 (
    .CLK(in_2), .DADOS(undriven), .SAIDA(registrador_de_dois_bits_2_saida));
  assign NAND = ~(registrador_de_dois_bits_1_saida & registrador_de_dois_bits_2_saida);  // NAND_Gate nand_1, 2 bits wide
  assign NOR = ~(registrador_de_dois_bits_1_saida | registrador_de_dois_bits_2_saida);  // NOR_Gate nor_1, 2 bits wide
  assign XNOR = ~(registrador_de_dois_bits_1_saida ^ registrador_de_dois_bits_2_saida);  // XNOR_Gate xnor_1, 2 bits wide

  // Notes on the sheet:
  //   Logical Unit
  //   Marcos Felipe Martins Silva-415719
endmodule
