// Logisim project Exercicio03_guia13.circ as structural Verilog: 5 circuits, main circuit registrador
module registrador (
  input  in_1,
  input  [1:0] in_2,
  output [1:0] out_3
);

  D_Flip_Flop #(.trigger("rising")) d_ff_1 (.clk(in_1), .D(in_2[0]), .Q(out_3[1]));  // open: Qn, preset, en, reset
  D_Flip_Flop #(.trigger("rising")) d_ff_2 (.clk(in_1), .D(in_2[1]), .Q(out_3[0]));  // open: Qn, preset, en, reset
endmodule

module igual (
  input  [1:0] in_1,
  input  [1:0] in_2,
  output out_3
);

  wire xnor_1_out, xnor_2_out;

  xnor xnor_1 (xnor_1_out, in_1[0], in_2[0]);
  xnor xnor_2 (xnor_2_out, in_1[1], in_2[1]);
  and and_1 (out_3, xnor_1_out, xnor_2_out);
endmodule

module menor (
  input  [1:0] in_1,
  input  [1:0] in_2,
  output out_3
);

  wire and_1_out, and_2_out, and_3_out;
  wire [1:0] not_1_out;

  assign not_1_out = ~in_1;  // NOT_Gate not_1, 2 bits wide
  and and_1 (and_1_out, not_1_out[1], in_2[1]);
  and and_2 (and_2_out, not_1_out[1], in_2[0], not_1_out[0]);
  and and_3 (and_3_out, not_1_out[0], in_2[0], in_2[1]);
  or or_1 (out_3, and_1_out, and_2_out, and_3_out);
endmodule

module maior (
  input  [1:0] in_1,
  input  [1:0] in_2,
  output out_3
);

  wire and_1_out, and_2_out, and_3_out;
  wire [1:0] not_1_out;

  assign not_1_out = ~in_2;  // NOT_Gate not_1, 2 bits wide
  and and_1 (and_1_out, in_1[1], not_1_out[1]);
  and and_2 (and_2_out, in_1[1], not_1_out[0], in_1[0]);
  and and_3 (and_3_out, in_1[0], not_1_out[0], not_1_out[1]);
  or or_1 (out_3, and_1_out, and_2_out, and_3_out);
endmodule

module LU (
  input  [1:0] a,
  input  [1:0] b,
  output iguais,
  output b___a,
  output a___b
);

  wire clock_1_out;
  wire [1:0] registrador_1_out_3, registrador_2_out_3;

  Clock #(.highDuration(1), .lowDuration(1)) clock_1 (.out(clock_1_out));
  registrador registrador_1 (.in_1(clock_1_out), .in_2(a), .out_3(registrador_1_out_3));
  registrador registrador_2 (.in_1(clock_1_out), .in_2(b), .out_3(registrador_2_out_3));
  igual igual_1 (.in_1(registrador_1_out_3), .in_2(registrador_2_out_3), .out_3(iguais));
  menor menor_1 (.in_1(registrador_1_out_3), .in_2(registrador_2_out_3), .out_3(b___a));
  maior maior_1 (.in_1(registrador_1_out_3), .in_2(registrador_2_out_3), .out_3(a___b));

  // Notes on the sheet:
  //   LU - comparador lógico
  //   Marcos Felipe Martins Silva-415719
endmodule
