// Logisim project Circ13_04.circ as structural Verilog: 2 circuits, main circuit registrador 4 bits
module registrador_4_bits (
  input  in_1,
  input  [3:0] in_2,
  output [3:0] out_3
);

  D_Flip_Flop #(.trigger("rising")) d_ff_1 (.clk(in_1), .D(in_2[0]), .Q(out_3[3]));  // open: Qn, preset, en, reset
  D_Flip_Flop #(.trigger("rising")) d_ff_2 (.clk(in_1), .D(in_2[1]), .Q(out_3[2]));  // open: Qn, preset, en, reset
  D_Flip_Flop #(.trigger("rising")) d_ff_3 (.clk(in_1), .D(in_2[2]), .Q(out_3[1]));  // open: Qn, preset, en, reset
  D_Flip_Flop #(.trigger("rising")) d_ff_4 (.clk(in_1), .D(in_2[3]), .Q(out_3[0]));  // open: Qn, preset, en, reset

  // Notes on the sheet:
  //   Igor Rodrigues de Oliveira - 380771 
endmodule

module LU_4bits (
  input  [3:0] in_1,
  input  [3:0] in_2,
  output [3:0] out_3,
  output [3:0] out_4,
  output [3:0] out_5,
  output [3:0] out_6,
  output [3:0] out_7,
  output [3:0] out_8,
  output [3:0] out_9,
  output [3:0] out_10
);

  wire clock_1_out;
  wire [3:0] registrador_4_bits_1_out_3, registrador_4_bits_2_out_3;

  Clock #(.highDuration(1), .lowDuration(1)) clock_1 (.out(clock_1_out));
  registrador_4_bits registrador_4_bits_1 (.in_1(clock_1_out), .in_2(in_1), .out_3(registrador_4_bits_1_out_3));
  registrador_4_bits registrador_4_bits_2 (.in_1(clock_1_out), .in_2(in_2), .out_3(registrador_4_bits_2_out_3));
  assign out_3 = ~registrador_4_bits_1_out_3;  // NOT_Gate not_1, 4 bits wide
  assign out_4 = ~registrador_4_bits_2_out_3;  // NOT_Gate not_2, 4 bits wide
  assign out_5 = registrador_4_bits_1_out_3 & registrador_4_bits_2_out_3;  // AND_Gate and_1, 4 bits wide
  assign out_6 = registrador_4_bits_1_out_3 | registrador_4_bits_2_out_3;  // OR_Gate or_1, 4 bits wide
  assign out_7 = ~(registrador_4_bits_1_out_3 & registrador_4_bits_2_out_3);  // NAND_Gate nand_1, 4 bits wide
  assign out_8 = ~(registrador_4_bits_1_out_3 | registrador_4_bits_2_out_3);  // NOR_Gate nor_1, 4 bits wide
  assign out_9 = registrador_4_bits_1_out_3 ^ registrador_4_bits_2_out_3;  // XOR_Gate xor_1, 4 bits wide
  assign out_10 = ~(registrador_4_bits_1_out_3 ^ registrador_4_bits_2_out_3);  // XNOR_Gate xnor_1, 4 bits wide

  // Notes on the sheet:
  //   Igor Rodrigues de Oliveira - 380771
endmodule
