// Logisim project Circ13_05.circ as structural Verilog: 1 circuit, main circuit guia12_5
module guia12_5 (
  output out_1,
  output out_2,
  output out_3
);

  wire clock_1_out, logisim_1_0_j_k_ff_1_p2, logisim_1_0_j_k_ff_1_p5;

  Clock #(.highDuration(1), .lowDuration(1)) clock_1 (.out(clock_1_out));
  // Logisim_1_0_J_K_Flip_Flop logisim_1_0_j_k_ff_1: pin names not known; wires that end beside it: 1'b1, logisim_1_0_j_k_ff_1_p2, 1'b1, out_2, logisim_1_0_j_k_ff_1_p5
  // Logisim_1_0_J_K_Flip_Flop logisim_1_0_j_k_ff_2: pin names not known; wires that end beside it: 1'b1, clock_1_out, 1'b1, out_3, logisim_1_0_j_k_ff_1_p2
  // Logisim_1_0_J_K_Flip_Flop logisim_1_0_j_k_ff_3: pin names not known; wires that end beside it: 1'b1, logisim_1_0_j_k_ff_1_p5, 1'b1, out_1

  // Notes on the sheet:
  //   Igor Rodrigues de Oliveira - 380771
endmodule
