// Logisim project Ex1301.circ as structural Verilog: 2 circuits, main circuit Registrador
module Registrador (
  input  CLK,
  input  [1:0] DADOS,
  output [1:0] SAIDA
);

  D_Flip_Flop #(.trigger("rising")) d_ff_1 (.clk(CLK), .D(DADOS[1]), .Q(SAIDA[1]));  // open: Qn, preset, en, reset
  D_Flip_Flop #(.trigger("rising")) d_ff_2 (.clk(CLK), .D(DADOS[0]), .Q(SAIDA[0]));  // open: Qn, preset, en, reset

  // Notes on the sheet:
  //   Júlio Cézar Taveira Araujo - 380776
endmodule

module Logical_Unit (
  input  [1:0] DADO1,
  input  [1:0] DADO2,
  output [1:0] out_3,
  output [1:0] out_4,
  output [1:0] out_5,
  output [1:0] out_6,
  output [1:0] out_7
);

  wire clock_1_out;
  wire [1:0] registrador_1_saida, registrador_2_saida;

  Clock #(.highDuration(1), .lowDuration(1)) clock_1 (.out(clock_1_out));
  Registrador registrador_1 (.CLK(clock_1_out), .DADOS(DADO1), .SAIDA(registrador_1_saida));
  Registrador registrador_2 (.CLK(clock_1_out), .DADOS(DADO2), .SAIDA(registrador_2_saida));
  assign out_3 = ~registrador_1_saida;  // NOT_Gate not_1, 2 bits wide
  assign out_5 = registrador_1_saida & registrador_2_saida;  // AND_Gate and_1, 2 bits wide
  assign out_4 = ~registrador_2_saida;  // NOT_Gate not_2, 2 bits wide
  assign out_6 = registrador_1_saida | registrador_1_saida;  // OR_Gate or_1, 2 bits wide
  assign out_7 = registrador_2_saida ^ registrador_1_saida;  // XOR_Gate xor_1, 2 bits wide
endmodule
