// Logisim project Ex1302.circ as structural Verilog: 2 circuits, main circuit Registrador
module Registrador (
  input  CLK,
  input  [1:0] DADOS,
  output [1:0] SAIDA
);

  D_Flip_Flop #(.trigger("rising")) d_ff_1 (.clk(CLK), .D(DADOS[0]), .Q(SAIDA[1]));  // open: Qn, preset, en, reset
  D_Flip_Flop #(.trigger("rising")) d_ff_2 (.clk(CLK), .D(DADOS[1]), .Q(SAIDA[0]));  // open: Qn, preset, en, reset

  // Notes on the sheet:
  //   Júlio Cézar Taveira Araújo - 380776
endmodule

module Logical_Unit (
  input  [1:0] DADOS1,
  input  in_2,
  input  [1:0] DADOS2,
  output [1:0] out_4,
  output [1:0] out_5,
  output [1:0] out_6
);

  wire [1:0] registrador_1_saida, registrador_2_saida;

  Registrador registrador_1 (.CLK(in_2), .DADOS(DADOS1), .SAIDA(registrador_1_saida));
  Registrador registrador_2 (.CLK(in_2), .DADOS(DADOS2), .SAIDA(registrador_2_saida));
  assign out_4 = ~(registrador_1_saida & registrador_2_saida);  // NAND_Gate nand_1, 2 bits wide
  assign out_5 = ~(registrador_1_saida | registrador_2_saida);  // NOR_Gate nor_1, 2 bits wide
  assign out_6 = ~(registrador_2_saida ^ registrador_1_saida);  // XNOR_Gate xnor_1, 2 bits wide
endmodule
