// Logisim project Ex1304.circ as structural Verilog: 2 circuits, main circuit Registrador
module Registrador (
  input  in_1,
  input  [3:0] in_2,
  output [3:0] out_3
);

  D_Flip_Flop #(.trigger("rising")) d_ff_1 (.clk(in_1), .D(in_2[0]), .Q(out_3[3]));  // open: Qn, preset, en, reset
  D_Flip_Flop #(.trigger("rising")) d_ff_2 (.clk(in_1), .D(in_2[1]), .Q(out_3[2]));  // open: Qn, preset, en, reset
  D_Flip_Flop #(.trigger("rising")) d_ff_3 (.clk(in_1), .D(in_2[2]), .Q(out_3[1]));  // open: Qn, preset, en, reset
  D_Flip_Flop #(.trigger("rising")) d_ff_4 (.clk(in_1), .D(in_2[3]), .Q(out_3[0]));  // open: Qn, preset, en, reset

  // Notes on the sheet:
  //   Júlio Cézar Taveira Araújo - 380776
endmodule

module LU (
  input  [3:0] in_1,
  input  [3:0] in_2,
  output [3:0] out_3,
  output [3:0] out_4,
  output [3:0] out_5,
  output [3:0] out_6,
  output [3:0] out_7,
  output [3:0] out_8,
  output [3:0] out_9,
  output [3:0] out_10
);

  wire clock_1_out;
  wire [3:0] registrador_1_out_3, registrador_2_out_3;

  Clock #(.highDuration(1), .lowDuration(1)) clock_1 (.out(clock_1_out));
  Registrador registrador_1 (.in_1(clock_1_out), .in_2(in_1), .out_3(registrador_1_out_3));
  Registrador registrador_2 (.in_1(clock_1_out), .in_2(in_2), .out_3(registrador_2_out_3));
  assign out_3 = ~registrador_1_out_3;  // NOT_Gate not_1, 4 bits wide
  assign out_4 = ~registrador_2_out_3;  // NOT_Gate not_2, 4 bits wide
  assign out_5 = registrador_1_out_3 & registrador_2_out_3;  // AND_Gate and_1, 4 bits wide
  assign out_6 = registrador_1_out_3 | registrador_2_out_3;  // OR_Gate or_1, 4 bits wide
  assign out_7 = ~(registrador_1_out_3 & registrador_2_out_3);  // NAND_Gate nand_1, 4 bits wide
  assign out_8 = ~(registrador_1_out_3 | registrador_2_out_3);  // NOR_Gate nor_1, 4 bits wide
  assign out_9 = registrador_1_out_3 ^ registrador_2_out_3;  // XOR_Gate xor_1, 4 bits wide
  assign out_10 = ~(registrador_1_out_3 ^ registrador_2_out_3);  // XNOR_Gate xnor_1, 4 bits wide
endmodule
