// Logisim project Ex1305.circ as structural Verilog: 1 circuit, main circuit Contador de Pulso
module Contador_de_Pulso (
  input  Clock,
  output out_2,
  output out_3,
  output out_4
);

  wire clock_1_out, j_k_ff_1_qn, j_k_ff_2_qn;

  Clock #(.highDuration(1), .lowDuration(1)) clock_1 (.out(clock_1_out));
  J_K_Flip_Flop #(.trigger("rising")) j_k_ff_1 (
    .J(1'b1), .clk(clock_1_out), .K(1'b1), .Q(out_4), .Qn(j_k_ff_1_qn), .reset(Clock));  // open: preset, en
  J_K_Flip_Flop #(.trigger("rising")) j_k_ff_2 (
    .J(1'b1), .clk(j_k_ff_1_qn), .K(1'b1), .Q(out_3), .Qn(j_k_ff_2_qn), .reset(Clock));  // open: preset, en
  J_K_Flip_Flop #(.trigger("rising")) j_k_ff_3 (
    .J(1'b1), .clk(j_k_ff_2_qn), .K(1'b1), .Q(out_2), .reset(Clock));  // open: Qn, preset, en

  // Notes on the sheet:
  //   Clear
  //   Júlio Cézar Taveira Araújo - 380776
endmodule
