// Logisim project Guia1305.circ as structural Verilog: 1 circuit, main circuit main
module main (
  input  in_1,
  input  in_2,
  output _1,
  output _2,
  output _4
);

  wire and_1_out, clock_1_out, j_k_ff_1_q, j_k_ff_2_q, j_k_ff_3_q, or_1_out;

  Clock #(.highDuration(1), .lowDuration(1)) clock_1 (.out(clock_1_out));
  J_K_Flip_Flop #(.trigger("rising")) j_k_ff_1 (
    .J(in_1), .clk(clock_1_out), .K(in_1), .Q(j_k_ff_1_q), .en(or_1_out));  // open: Qn, preset, reset
  not not_1 (_1, j_k_ff_1_q);
  and and_1 (and_1_out, j_k_ff_2_q, j_k_ff_1_q, j_k_ff_3_q);
  J_K_Flip_Flop #(.trigger("rising")) j_k_ff_2 (
    .J(in_1), .clk(j_k_ff_1_q), .K(in_1), .Q(j_k_ff_2_q), .en(or_1_out));  // open: Qn, preset, reset
  or or_1 (or_1_out, and_1_out, in_2);
  not not_2 (_2, j_k_ff_2_q);
  J_K_Flip_Flop #(.trigger("rising")) j_k_ff_3 (
    .J(in_1), .clk(j_k_ff_2_q), .K(in_1), .Q(j_k_ff_3_q), .en(or_1_out));  // open: Qn, preset, reset
  not not_3 (_4, j_k_ff_3_q);

  // Notes on the sheet:
  //   1
  //   Contador crescente de 3 bits
  //   Andre Sulivam 391998
  //   4
endmodule
