// Logisim project circuito_LU_tipoD_dois.circ as structural Verilog: 1 circuit, main circuit circuito__LU_tipoD_dois.circ
module circuito__LU_tipoD_dois_circ (
  input  entrada1,
  input  clier,
  input  in_3,
  output out_4,
  output out_5,
  output out_6
);

  wire clock_1_out, d_ff_1_qn, d_ff_2_qn, nand_1_out, nor_1_out;

  Clock #(.highDuration(1), .lowDuration(1)) clock_1 (.out(clock_1_out));
  not nand_1 (nand_1_out, entrada1);  // NAND_Gate
  D_Flip_Flop #(.trigger("rising")) d_ff_1 (
    .clk(clock_1_out), .D(d_ff_1_qn), .Q(out_4), .Qn(d_ff_1_qn), .en(clier), .reset(nand_1_out));  // open: preset
  D_Flip_Flop #(.trigger("rising")) d_ff_2 (
    .clk(clock_1_out), .D(d_ff_2_qn), .Q(out_6), .Qn(d_ff_2_qn), .en(clier), .reset(nor_1_out));  // open: preset
  not nor_1 (nor_1_out, in_3);  // NOR_Gate
  xor xor_1 (out_5, out_4, out_6);

  // Notes on the sheet:
  //   clock
  //   entrada2
  //   REVER COMENTARIOS ANTERIORES
  //   circuito Logical Unit de 2 bits
  //   com operaçoes NAND ,NOR,XNOR
  //   Nome: Eneas
  //   matricula:376507
endmodule
