// Logisim project circuito_logicalLU_tres.circ as structural Verilog: 1 circuit, main circuit circuito_logicalLU_tres.circ
module circuito_logicalLU_tres_circ (
  input  entrada1,
  input  clier,
  input  in_3,
  output out_4,
  output out_5
);

  wire clock_1_out, d_ff_1_qn, d_ff_2_qn;

  Clock #(.highDuration(1), .lowDuration(1)) clock_1 (.out(clock_1_out));
  D_Flip_Flop #(.trigger("rising")) d_ff_1 (
    .clk(clock_1_out), .D(d_ff_1_qn), .Q(out_4), .Qn(d_ff_1_qn), .en(clier), .reset(entrada1));  // open: preset
  D_Flip_Flop #(.trigger("rising")) d_ff_2 (
    .clk(clock_1_out), .D(d_ff_2_qn), .Q(out_5), .Qn(d_ff_2_qn), .en(clier), .reset(in_3));  // open: preset
  Comparator #(.width(8), .mode("twosComplement")) comparator_1 (.gt(out_4), .lt(out_5));  // open: a, b, eq

  // Notes on the sheet:
  //   clock
  //   entrada2
  //   cicuito logical Unit LU de 2 bits com
  //   comparador
  //   colocando uma das entradas em 1
  //   subindo o clier para 1 e ocilar com o clock
  //   a cada dois pulsos de clock alterna o sinal
  //   quando abaixa o clier mantem o valor anterior
  //   se as duas entradas tiverem em 1 alterna o valor 
  //   a debaixo vai paracima e de cima para baixo
  //   VER COMENTÁRIO NO EXERCICIO ANTERIOR
  //   NAO HÁ ENTRADAS NO COMPARADOR
  //   Nome:Eneas
  //   Numero : 376507
endmodule
