// Logisim project circuito_logical_Unit_LU.circ as structural Verilog: 1 circuit, main circuit ciicito_logical_Unit_LU.circ
module ciicito_logical_Unit_LU_circ (
  input  entrada1,
  input  clier,
  input  entrada2,
  output out_4,
  output out_5
);

  wire and_1_out, clock_1_out, d_ff_1_qn, d_ff_2_qn, not_1_out, or_1_out, xor_1_out;

  Clock #(.highDuration(1), .lowDuration(1)) clock_1 (.out(clock_1_out));
  not not_1 (not_1_out, entrada1);
  D_Flip_Flop #(.trigger("rising")) d_ff_1 (
    .clk(clock_1_out), .D(d_ff_1_qn), .Q(out_4), .Qn(d_ff_1_qn), .en(clier), .reset(and_1_out));  // open: preset
  D_Flip_Flop #(.trigger("rising")) d_ff_2 (
    .clk(clock_1_out), .D(d_ff_2_qn), .Q(out_5), .Qn(d_ff_2_qn), .en(clier), .reset(xor_1_out));  // open: preset
  buf or_1 (or_1_out, entrada2);  // OR_Gate
  buf and_1 (and_1_out, not_1_out);  // AND_Gate
  buf xor_1 (xor_1_out, or_1_out);  // XOR_Gate

  // Notes on the sheet:
  //   clock
  //   circuito Logical Unit
  //   // NAO PODERÁ MANTER ESSA CONEXÃO, NAO VAI ENTRAR DADO
  //   quando a entrada e 1 e clier e 1 guarda o valor
  //   abaixando o cier para zero mantem
  //   a medida que ocila o clok vai trocando os valores de saida
  //   Nome;Eneas
  //   Numero:376507
endmodule
