// Logisim project guia13.circ as structural Verilog: 6 circuits, main circuit main
module main (
  input  [1:0] in_1,
  input  [1:0] in_2,
  input  [2:0] in_3,
  input  [3:0] in_4,
  output [1:0] out_5
);

  wire clock_1_out;
  wire [1:0] a_b_1_saida, a_b_2_saida, a_b_3_saida, and_1_out, multiplexer_1_out, nand_1_out, nor_1_out,
       not_1_out, or_1_out, registrador_1_saida, registrador_2_saida, xnor_1_out, xor_1_out;

  Clock #(.highDuration(1), .lowDuration(1)) clock_1 (.out(clock_1_out));
  registrador registrador_1 (.clock(clock_1_out), .entrada(in_1), .enable(in_3[0]), .saida(registrador_1_saida));
  registrador registrador_2 (.clock(clock_1_out), .entrada(in_2), .enable(in_3[1]), .saida(registrador_2_saida));
  assign not_1_out = ~registrador_2_saida;  // NOT_Gate not_1, 2 bits wide
  assign xor_1_out = registrador_1_saida ^ registrador_2_saida;  // XOR_Gate xor_1, 2 bits wide
  assign and_1_out = registrador_2_saida & registrador_1_saida;  // AND_Gate and_1, 2 bits wide
  assign or_1_out = registrador_2_saida | registrador_1_saida;  // OR_Gate or_1, 2 bits wide
  assign nand_1_out = ~(registrador_2_saida & registrador_1_saida);  // NAND_Gate nand_1, 2 bits wide
  assign nor_1_out = ~(registrador_2_saida | registrador_1_saida);  // NOR_Gate nor_1, 2 bits wide
  assign xnor_1_out = ~(registrador_2_saida ^ registrador_1_saida);  // XNOR_Gate xnor_1, 2 bits wide
  A___B a_b_1 (.a(registrador_2_saida), .b(registrador_1_saida), .Saida(a_b_1_saida));
  A___B_2_2 a_b_2 (.in_1(registrador_2_saida), .in_2(registrador_1_saida), .Saida(a_b_2_saida));
  A___B_2 a_b_3 (.in_1(registrador_2_saida), .in_2(registrador_1_saida), .Saida(a_b_3_saida));
  Multiplexer #(.select(4), .width(2)) multiplexer_1 (
    .in1(not_1_out), .in2(xor_1_out), .in3(and_1_out), .in4(or_1_out), .in5(nand_1_out), .in6(nor_1_out),
    .in12(xnor_1_out), .in13(a_b_1_saida), .in14(a_b_2_saida), .in15(a_b_3_saida), .out(multiplexer_1_out),
    .sel(in_4));  // open: in0, in7, in8, in9, in10, in11
  registrador registrador_3 (.clock(clock_1_out), .entrada(multiplexer_1_out), .enable(in_3[2]), .saida(out_5));
endmodule

module registrador (
  input  clock,
  input  [1:0] entrada,
  input  enable,
  output [1:0] saida
);

  D_Flip_Flop #(.trigger("rising")) d_ff_1 (
    .clk(clock), .D(entrada[0]), .Q(saida[0]), .en(enable));  // open: Qn, preset, reset
  D_Flip_Flop #(.trigger("rising")) d_ff_2 (
    .clk(clock), .D(entrada[1]), .Q(saida[1]), .en(enable));  // open: Qn, preset, reset
endmodule

module A___B (
  input  [1:0] a,
  input  [1:0] b,
  output [1:0] Saida
);

  wire and_1_out, and_2_out, and_3_out, and_4_out, not_1_out, not_2_out, not_3_out, not_4_out, not_5_out,
       not_6_out, not_7_out, not_8_out;

  not not_1 (not_1_out, a[1]);
  not not_2 (not_2_out, a[0]);
  not not_3 (not_3_out, b[0]);
  not not_4 (not_4_out, b[1]);
  not not_5 (not_5_out, a[0]);
  not not_6 (not_6_out, b[0]);
  not not_7 (not_7_out, a[0]);
  not not_8 (not_8_out, b[0]);
  and and_1 (and_1_out, not_1_out, not_2_out, not_3_out, not_4_out);
  and and_2 (and_2_out, a[1], not_5_out, b[1], not_6_out);
  and and_3 (and_3_out, a[1], a[0], b[1], b[0]);
  and and_4 (and_4_out, not_7_out, a[1], not_8_out, b[1]);
  or or_1 (Saida[1], and_2_out, and_1_out, and_3_out, and_4_out);

  assign Saida[0] = Saida[1];
endmodule

module A___B_2 (
  input  [1:0] in_1,
  input  [1:0] in_2,
  output [1:0] Saida
);

  wire and_1_out, and_2_out, and_3_out, and_4_out, and_5_out, and_6_out, not_1_out, not_2_out, not_3_out,
       not_4_out, not_5_out, not_6_out, not_7_out, not_8_out, not_9_out, not_10_out, not_11_out, not_12_out;

  not not_1 (not_1_out, in_1[1]);
  and and_1 (and_1_out, not_1_out, in_1[0], not_2_out, not_3_out);
  not not_2 (not_2_out, in_2[0]);
  not not_3 (not_3_out, in_1[0]);
  not not_4 (not_4_out, in_1[0]);
  and and_2 (and_2_out, in_1[1], not_4_out, not_5_out, not_6_out);
  not not_5 (not_5_out, in_1[0]);
  not not_6 (not_6_out, in_2[0]);
  and and_3 (and_3_out, in_1[1], in_1[0], not_7_out, not_8_out);
  not not_7 (not_7_out, in_1[0]);
  not not_8 (not_8_out, in_2[0]);
  not not_9 (not_9_out, in_1[0]);
  and and_4 (and_4_out, in_1[1], not_9_out, not_10_out, in_2[0]);
  not not_10 (not_10_out, in_1[0]);
  and and_5 (and_5_out, in_1[1], in_1[0], not_11_out, in_2[0]);
  not not_11 (not_11_out, in_1[0]);
  and and_6 (and_6_out, in_1[1], in_1[0], in_1[0], not_12_out);
  not not_12 (not_12_out, in_2[0]);
  or or_1 (Saida[1], and_1_out, and_2_out, and_3_out, and_4_out, and_5_out, and_6_out);

  assign in_2[1] = in_1[0];
  assign Saida[0] = Saida[1];
endmodule

module A___B_2_2 (
  input  [1:0] in_1,
  input  [1:0] in_2,
  output [1:0] Saida
);

  wire and_1_out, and_2_out, and_3_out, and_4_out, and_5_out, and_6_out, not_1_out, not_2_out, not_3_out,
       not_4_out, not_5_out, not_6_out, not_7_out, not_8_out, not_9_out, not_10_out, not_11_out, not_12_out;

  not not_1 (not_1_out, in_1[1]);
  and and_1 (and_1_out, not_1_out, not_2_out, in_2[0], not_3_out);
  not not_2 (not_2_out, in_1[0]);
  not not_3 (not_3_out, in_1[0]);
  not not_4 (not_4_out, in_1[1]);
  and and_2 (and_2_out, not_4_out, not_5_out, in_1[0], not_6_out);
  not not_5 (not_5_out, in_1[0]);
  not not_6 (not_6_out, in_2[0]);
  not not_7 (not_7_out, in_2[0]);
  and and_3 (and_3_out, not_7_out, in_1[0], in_1[1], not_8_out);
  not not_8 (not_8_out, in_1[0]);
  not not_9 (not_9_out, in_2[0]);
  not not_10 (not_10_out, in_1[0]);
  and and_4 (and_4_out, not_9_out, not_10_out, in_1[1], in_1[0]);
  not not_11 (not_11_out, in_2[0]);
  and and_5 (and_5_out, not_11_out, in_1[0], in_1[1], in_1[0]);
  not not_12 (not_12_out, in_1[0]);
  and and_6 (and_6_out, in_2[0], not_12_out, in_1[1], in_1[0]);
  or or_1 (Saida[1], and_1_out, and_2_out, and_3_out, and_4_out, and_5_out, and_6_out);

  assign in_2[1] = in_1[0];
  assign Saida[0] = Saida[1];
endmodule

module LU_2bits (
  input  [1:0] in_1,
  input  [1:0] in_2,
  input  [2:0] in_3,
  input  [3:0] in_4,
  output [1:0] out_5
);

  wire clock_1_out;
  wire [1:0] a_b_1_saida, a_b_2_saida, a_b_3_saida, and_1_out, multiplexer_1_out, nand_1_out, nor_1_out,
       not_1_out, or_1_out, registrador_1_saida, registrador_2_saida, xnor_1_out, xor_1_out;

  Clock #(.highDuration(1), .lowDuration(1)) clock_1 (.out(clock_1_out));
  registrador registrador_1 (.clock(clock_1_out), .entrada(in_1), .enable(in_3[0]), .saida(registrador_1_saida));
  registrador registrador_2 (.clock(clock_1_out), .entrada(in_2), .enable(in_3[1]), .saida(registrador_2_saida));
  assign not_1_out = ~registrador_2_saida;  // NOT_Gate not_1, 2 bits wide
  assign xor_1_out = registrador_1_saida ^ registrador_2_saida;  // XOR_Gate xor_1, 2 bits wide
  assign and_1_out = registrador_2_saida & registrador_1_saida;  // AND_Gate and_1, 2 bits wide
  assign or_1_out = registrador_2_saida | registrador_1_saida;  // OR_Gate or_1, 2 bits wide
  assign nand_1_out = ~(registrador_2_saida & registrador_1_saida);  // NAND_Gate nand_1, 2 bits wide
  assign nor_1_out = ~(registrador_2_saida | registrador_1_saida);  // NOR_Gate nor_1, 2 bits wide
  assign xnor_1_out = ~(registrador_2_saida ^ registrador_1_saida);  // XNOR_Gate xnor_1, 2 bits wide
  A___B a_b_1 (.a(registrador_2_saida), .b(registrador_1_saida), .Saida(a_b_1_saida));
  A___B_2_2 a_b_2 (.in_1(registrador_2_saida), .in_2(registrador_1_saida), .Saida(a_b_2_saida));
  A___B_2 a_b_3 (.in_1(registrador_2_saida), .in_2(registrador_1_saida), .Saida(a_b_3_saida));
  Multiplexer #(.select(4), .width(2)) multiplexer_1 (
    .in1(not_1_out), .in2(xor_1_out), .in3(and_1_out), .in4(or_1_out), .in5(nand_1_out), .in6(nor_1_out),
    .in12(xnor_1_out), .in13(a_b_1_saida), .in14(a_b_2_saida), .in15(a_b_3_saida), .out(multiplexer_1_out),
    .sel(in_4));  // open: in0, in7, in8, in9, in10, in11
  registrador registrador_3 (.clock(clock_1_out), .entrada(multiplexer_1_out), .enable(in_3[2]), .saida(out_5));
endmodule
