// Logisim project LU(4Bits).circ as structural Verilog: 10 circuits, main circuit Registrador4bits
module Registrador4bits (
  input  Clock,
  input  [3:0] Variavel,
  input  [7:0] DataPath,
  output [3:0] S
);

  wire d_ff_1_q, d_ff_2_q, d_ff_3_q, d_ff_4_q;

  D_Flip_Flop #(.trigger("rising")) d_ff_1 (
    .clk(Clock), .D(Variavel[3]), .Q(d_ff_1_q), .en(DataPath[7]));  // open: Qn, preset, reset
  D_Flip_Flop #(.trigger("rising")) d_ff_2 (
    .clk(Clock), .D(Variavel[2]), .Q(d_ff_2_q), .en(DataPath[5]));  // open: Qn, preset, reset
  D_Flip_Flop #(.trigger("rising")) d_ff_3 (
    .clk(Clock), .D(Variavel[1]), .Q(d_ff_3_q), .en(DataPath[3]));  // open: Qn, preset, reset
  D_Flip_Flop #(.trigger("rising")) d_ff_4 (
    .clk(Clock), .D(Variavel[0]), .Q(d_ff_4_q), .en(DataPath[1]));  // open: Qn, preset, reset
  assign S[3] = DataPath[6] ? d_ff_1_q : 1'bz;  // Controlled_Buffer controlled_buffer_1
  assign S[2] = DataPath[4] ? d_ff_2_q : 1'bz;  // Controlled_Buffer controlled_buffer_2
  assign S[1] = DataPath[2] ? d_ff_3_q : 1'bz;  // Controlled_Buffer controlled_buffer_3
  assign S[0] = DataPath[0] ? d_ff_4_q : 1'bz;  // Controlled_Buffer controlled_buffer_4

  // Notes on the sheet:
  //   Nádia de Souza Maciel Vieira Ferreira
endmodule

module LU4Bits (
  input  [3:0] A,
  input  [7:0] EA3_LoA3_EA2_LoA2_EA1_LoA1_EA0_LoA0,
  input  [3:0] B,
  input  [7:0] EB3_LoB3_EB2_LoB2_EB1_LoB1_EB0_LoB0,
  input  [3:0] Chave,
  output [3:0] out_6
);

  wire Clock_out;
  wire [0:0] comparadorlogico_1_out_3, comparadorlogico_1_out_4, comparadorlogico_1_out_5;
  wire [3:0] and4bits_1_s, nand4bits_1_s, nor4bits_1_s, not4bits_1_x_prime, not4bits_2_x_prime, or4bits_1_s,
       registrador4bits_1_s, registrador4bits_2_s, xnor4bits_1_s, xor4bits_1_s;

  Clock #(.highDuration(1), .lowDuration(1)) Clock (.out(Clock_out));
  Registrador4bits registrador4bits_1 (
    .Clock(Clock_out), .Variavel(A), .DataPath(EA3_LoA3_EA2_LoA2_EA1_LoA1_EA0_LoA0), .S(registrador4bits_1_s));
  Registrador4bits registrador4bits_2 (
    .Clock(Clock_out), .Variavel(B), .DataPath(EB3_LoB3_EB2_LoB2_EB1_LoB1_EB0_LoB0), .S(registrador4bits_2_s));
  Not4Bits not4bits_1 (.X(registrador4bits_1_s), .X_prime(not4bits_1_x_prime));
  Not4Bits not4bits_2 (.X(registrador4bits_2_s), .X_prime(not4bits_2_x_prime));
  And4Bits and4bits_1 (.A(registrador4bits_1_s), .B(registrador4bits_2_s), .S(and4bits_1_s));
  Or4Bits or4bits_1 (.A(registrador4bits_1_s), .B(registrador4bits_2_s), .S(or4bits_1_s));
  Xor4Bits xor4bits_1 (.A(registrador4bits_1_s), .B(registrador4bits_2_s), .S(xor4bits_1_s));
  Nand4Bits nand4bits_1 (.A(registrador4bits_1_s), .B(registrador4bits_2_s), .S(nand4bits_1_s));
  Nor4Bits nor4bits_1 (.A(registrador4bits_1_s), .B(registrador4bits_2_s), .S(nor4bits_1_s));
  Xnor4Bits xnor4bits_1 (.A(registrador4bits_1_s), .B(registrador4bits_2_s), .S(xnor4bits_1_s));
  ComparadorLogico comparadorlogico_1 (
    .A(registrador4bits_1_s), .B(registrador4bits_2_s), .out_3(comparadorlogico_1_out_3[0]),
    .out_4(comparadorlogico_1_out_4[0]), .out_5(comparadorlogico_1_out_5[0]));
  Multiplexer #(.select(4), .width(4)) multiplexer_1 (
    .in0(not4bits_1_x_prime), .in1(not4bits_2_x_prime), .in2(and4bits_1_s), .in3(or4bits_1_s),
    .in4(xor4bits_1_s), .in5(nand4bits_1_s), .in6(nor4bits_1_s), .in7(xnor4bits_1_s),
    .in8({3'b000, comparadorlogico_1_out_3[0]}), .in9({3'b000, comparadorlogico_1_out_4[0]}),
    .in10({3'b000, comparadorlogico_1_out_5[0]}), .out(out_6), .sel(Chave));  // open: in11, in12, in13, in14, in15

  // Notes on the sheet:
  //   Tabela De Chaves
  //   0000 - Not A
  //   0001 - Not B
  //   0010 - AND
  //   0011 - Or
  //   0100 - Xor
  //   0101 - Nand
  //   0110 - Nor
  //   0111 - Xnor
  //   1000 - B < A
  //   1001 - B = A
  //   1010 - B > A
  //   Nádia de Souza Maciel Vieira Ferreira
  //   Not A
  //   Not B
  //   And
  //   Or
  //   Xor
  //   Nand
  //   Nor
  //   Xnor
  //   <=>
endmodule

module Xor4Bits (
  input  [3:0] A,
  input  [3:0] B,
  output [3:0] S
);

  assign S = A ^ B;  // XOR_Gate xor_1, 4 bits wide

  // Notes on the sheet:
  //   Nádia de Souza Maciel Vieira Ferreira
endmodule

module Not4Bits (
  input  [3:0] X,
  output [3:0] X_prime
);

  assign X_prime = ~X;  // NOT_Gate not_1, 4 bits wide

  // Notes on the sheet:
  //   Nádia de Souza Maciel Vieira Ferreira
endmodule

module And4Bits (
  input  [3:0] A,
  input  [3:0] B,
  output [3:0] S
);

  assign S = A & B;  // AND_Gate and_1, 4 bits wide

  // Notes on the sheet:
  //   Nádia de Souza Maciel Vieira Ferreira
endmodule

module Or4Bits (
  input  [3:0] A,
  input  [3:0] B,
  output [3:0] S
);

  assign S = A | B;  // OR_Gate or_1, 4 bits wide

  // Notes on the sheet:
  //   Nádia de Souza Maciel Vieira Ferreira
endmodule

module Nand4Bits (
  input  [3:0] A,
  input  [3:0] B,
  output [3:0] S
);

  assign S = ~(A & B);  // NAND_Gate nand_1, 4 bits wide

  // Notes on the sheet:
  //   Nádia de Souza Maciel Vieira Ferreira
endmodule

module Nor4Bits (
  input  [3:0] A,
  input  [3:0] B,
  output [3:0] S
);

  assign S = ~(A | B);  // NOR_Gate nor_1, 4 bits wide

  // Notes on the sheet:
  //   Nádia de Souza Maciel Vieira Ferreira
endmodule

module Xnor4Bits (
  input  [3:0] A,
  input  [3:0] B,
  output [3:0] S
);

  assign S = ~(A ^ B);  // XNOR_Gate xnor_1, 4 bits wide

  // Notes on the sheet:
  //   Nádia de Souza Maciel Vieira Ferreira
endmodule

module ComparadorLogico (
  input  [3:0] A,
  input  [3:0] B,
  output out_3,
  output out_4,
  output out_5
);

  Comparator #(.width(4), .mode("twosComplement")) comparator_1 (.a(A), .b(B), .gt(out_3), .eq(out_4), .lt(out_5));

  // Notes on the sheet:
  //   Nádia de SOuza Maciel Vieira Ferreira
endmodule
