// Logisim project circ_MemoraRam1X8.circ as structural Verilog: 1 circuit, main circuit circ_MemoriaRam1X8.circ
module circ_MemoriaRam1X8_circ (
  input  entrada1,
  input  clock,
  input  clier,
  input  entrada3,
  input  entrada4
);

  wire clock_1_out, d_ff_1_q, d_ff_1_qn, d_ff_2_q, d_ff_2_qn, d_ff_3_q, d_ff_3_qn, d_ff_4_q, d_ff_4_qn,
       or_1_out, or_2_out;

  Clock #(.highDuration(1), .lowDuration(1)) clock_1 (.out(clock_1_out));
  D_Flip_Flop #(.trigger("rising")) d_ff_1 (
    .clk(clock_1_out), .D(d_ff_1_qn), .Q(d_ff_1_q), .Qn(d_ff_1_qn), .en(clier), .reset(entrada1));  // open: preset
  D_Flip_Flop #(.trigger("rising")) d_ff_2 (
    .clk(clock_1_out), .D(d_ff_2_qn), .Q(d_ff_2_q), .Qn(d_ff_2_qn), .en(clier), .reset(clock));  // open: preset
  D_Flip_Flop #(.trigger("rising")) d_ff_3 (
    .clk(clock_1_out), .D(d_ff_3_qn), .Q(d_ff_3_q), .Qn(d_ff_3_qn), .en(clier), .reset(entrada3));  // open: preset
  D_Flip_Flop #(.trigger("rising")) d_ff_4 (
    .clk(clock_1_out), .D(d_ff_4_qn), .Q(d_ff_4_q), .Qn(d_ff_4_qn), .en(clier), .reset(entrada4));  // open: preset
  or or_1 (or_1_out, d_ff_3_q, d_ff_4_q);
  or or_2 (or_2_out, d_ff_1_q, d_ff_2_q);
  RAM #(.addrWidth(8), .dataWidth(8), .bus("combined")) ram_1 (
    .sel(or_1_out), .clk(clock_1_out), .ld(or_2_out));  // open: addr, data, clr

  // Notes on the sheet:
  //   entrada2
  //   circuito memoria Ram 4X8 usando memoria1X8
  //   NAO RECEBE DADO
  //   NAO PODERÁ FAZER ESSA CONEXAO
  //   Nome:Eneas
  //   Matricula :376507
endmodule
