// Logisim project circuito_MemoriaRam_1X2.circ as structural Verilog: 1 circuit, main circuit circuito_MemoriaRam_1X2.circ
module circuito_MemoriaRam_1X2_circ (
  input  entrada1,
  input  clier,
  input  entrada2,
  output out_4,
  output out_5
);

  wire clock_1_out, d_ff_1_qn, d_ff_2_qn;

  Clock #(.highDuration(1), .lowDuration(1)) clock_1 (.out(clock_1_out));
  D_Flip_Flop #(.trigger("rising")) d_ff_1 (
    .clk(clock_1_out), .D(d_ff_1_qn), .Q(out_4), .Qn(d_ff_1_qn), .en(clier), .reset(entrada1));  // open: preset
  D_Flip_Flop #(.trigger("rising")) d_ff_2 (
    .clk(clock_1_out), .D(d_ff_2_qn), .Q(out_5), .Qn(d_ff_2_qn), .en(clier), .reset(entrada2));  // open: preset
  RAM #(.addrWidth(8), .dataWidth(8), .bus("combined")) ram_1 (
    .sel(out_5), .clk(clock_1_out), .ld(out_4), .clr(clier));  // open: addr, data

  // Notes on the sheet:
  //   clock
  //   circuito
  //   Memoria Ram 1X4
  //   toda vez que o clier vai para 1 e tem oScilaçoes de clock
  //   o flipflop tipo de armazena o dado
  //   quando o clier vai para 0 o dado permanece guardado
  //   se mudar o clier para um novamente ,torca o dado na memoria
  //   registrador
  //   VER COMENTARIO NO EX. 1
  //   OS FLIP-FLOPS SERVIRAO PARA MONTAR A MEMORIA
  //   Nome :Eneas
  //   Numero :376507
endmodule
