// Logisim project circuito_MemoriaRam_1X8.circ as structural Verilog: 1 circuit, main circuit circuito_MemoriaRam_1X8.circ
module circuito_MemoriaRam_1X8_circ (
  input  entrada1,
  input  clier,
  input  in_3,
  output out_4,
  output out_5
);

  wire clock_1_out, d_ff_1_q, d_ff_1_qn, d_ff_2_qn;

  Clock #(.highDuration(1), .lowDuration(1)) clock_1 (.out(clock_1_out));
  D_Flip_Flop #(.trigger("rising")) d_ff_1 (
    .clk(clock_1_out), .D(d_ff_1_qn), .Q(d_ff_1_q), .Qn(d_ff_1_qn), .en(clier));  // open: preset, reset
  D_Flip_Flop #(.trigger("rising")) d_ff_2 (
    .clk(clock_1_out), .D(d_ff_2_qn), .Q(out_5), .Qn(d_ff_2_qn), .en(clier), .reset(in_3));  // open: preset
  or or_1 (out_4, d_ff_1_q, out_5);
  RAM #(.addrWidth(8), .dataWidth(8), .bus("combined")) ram_1 (
    .sel(out_5), .clk(clock_1_out), .ld(out_4), .clr(clier));  // open: addr, data

  // Notes on the sheet:
  //   clock
  //   entrada2
  //   com a ocilaçao do clok
  //   VER COMENTARIOS NOS EXERCICIOS ANTERIORES
  //   circuito memoria Ram 1X8 usando memoria 1X4
  //   mantendo o clier em 1 e as entradas em zero alterna nos tipos d entre eles
  //   uma das entradas em 1 e o clier em 1 pega o valor fornecido e lela para a memoria
  //   zerando o clier mantem guardado os dados até que o clier volte para 1
  //   Nome :Eneas
  //   Matricula :376507
endmodule
