// Logisim project Guia14.circ as structural Verilog: 9 circuits, main circuit registrador-D
module registrador_D (
  input  [3:0] dado,
  input  clk,
  output [3:0] out_3
);

  D_Flip_Flop #(.trigger("rising")) d_ff_1 (.clk(clk), .D(dado[3]), .Q(out_3[3]));  // open: Qn, preset, en, reset
  D_Flip_Flop #(.trigger("rising")) d_ff_2 (.clk(clk), .D(dado[2]), .Q(out_3[2]));  // open: Qn, preset, en, reset
  D_Flip_Flop #(.trigger("rising")) d_ff_3 (.clk(clk), .D(dado[1]), .Q(out_3[1]));  // open: Qn, preset, en, reset
  D_Flip_Flop #(.trigger("rising")) d_ff_4 (.clk(clk), .D(dado[0]), .Q(out_3[0]));  // open: Qn, preset, en, reset

  // Notes on the sheet:
  //   Registrador 4bits
  //   Celso R Franca Jr
endmodule

module Memoria_1x4_D (
  input  [3:0] Dados___in,
  input  R_W,
  input  cs,
  input  clk,
  output [3:0] Data___out
);

  wire and_1_out, and_2_out, not_1_out;
  wire [3:0] controlled_buffer_2_out, registrador_d_1_out_3;

  not not_1 (not_1_out, R_W);
  and and_1 (and_1_out, not_1_out, cs);
  and and_2 (and_2_out, cs, R_W);
  assign Data___out = and_2_out ? registrador_d_1_out_3 : 4'bz;  // Controlled_Buffer controlled_buffer_1
  registrador_D registrador_d_1 (.dado(controlled_buffer_2_out), .clk(clk), .out_3(registrador_d_1_out_3));
  assign controlled_buffer_2_out = and_1_out ? Dados___in : 4'bz;  // Controlled_Buffer controlled_buffer_2

  // Notes on the sheet:
  //   R/W 
  //   1 - leitura
  //   0 - escrita
  //   CS
  //   Memoria 1x4
  //   habilita a gravação
  //   ou a escrita
  //   1 - habilitado
  //   0 - desabilitado
  //   obs:
  //   Celso R Franca Jr
  //   registradores de 4bits 
  //   usando Flip-Flops do tipo D
endmodule

module Memoria_1x8_D (
  input  [7:0] in_1,
  input  R_W,
  input  cs,
  input  clk,
  output [7:0] out_5
);

  Memoria_1x4_D memoria_1x4_d_1 (.R_W(R_W), .cs(cs), .clk(clk), .Dados___in(in_1[3:0]), .Data___out(out_5[3:0]));
  Memoria_1x4_D memoria_1x4_d_2 (.R_W(R_W), .cs(cs), .clk(clk), .Dados___in(in_1[7:4]), .Data___out(out_5[7:4]));

  // Notes on the sheet:
  //   1 - leitura
  //   0 - escrita
  //   R/W 
  //   Memoria 1x8
  //   CS
  //   ou a escrita
  //   1 - habilitado
  //   0 - desabilitado
  //   habilita a gravação
  //   obs:
  //   registradores de 4bits 
  //   usando Flip-Flops do tipo D
  //   Celso R Franca Jr
endmodule

module Memoria_4x8_D (
  input  [7:0] dados___in,
  input  R_W,
  input  clk,
  input  cs,
  input  [1:0] \endereçamento ,
  output [7:0] dados___out
);

  wire demultiplexer_1_out0, demultiplexer_1_out1, demultiplexer_1_out2, demultiplexer_1_out3;

  Demultiplexer #(.select(2), .width(1), .tristate("false")) demultiplexer_1 (
    .out0(demultiplexer_1_out0), .out1(demultiplexer_1_out1), .out2(demultiplexer_1_out2),
    .out3(demultiplexer_1_out3), .in(cs), .sel(\endereçamento ));
  Memoria_1x8_D memoria_1x8_d_1 (
    .R_W(R_W), .cs(demultiplexer_1_out0), .clk(clk), .in_1(dados___in), .out_5(dados___out));
  Memoria_1x8_D memoria_1x8_d_2 (
    .R_W(R_W), .cs(demultiplexer_1_out1), .clk(clk), .in_1(dados___in), .out_5(dados___out));
  Memoria_1x8_D memoria_1x8_d_3 (
    .R_W(R_W), .cs(demultiplexer_1_out2), .clk(clk), .in_1(dados___in), .out_5(dados___out));
  Memoria_1x8_D memoria_1x8_d_4 (
    .R_W(R_W), .cs(demultiplexer_1_out3), .clk(clk), .in_1(dados___in), .out_5(dados___out));

  // Notes on the sheet:
  //   R/W 
  //   1 - leitura
  //   0 - escrita
  //   CS
  //   ou a escrita
  //   1 - habilitado
  //   Memoria 4x8
  //   habilita a gravação
  //   0 - desabilitado
  //   Celso R Franca Jr
  //   obs:
  //   registradores de 8bits 
  //   usando Flip-Flops do tipo D
endmodule

module registrador__JK (
  input  [3:0] dado,
  input  clk,
  output [3:0] out_3
);

  wire not_1_out, not_2_out, not_3_out, not_4_out;

  J_K_Flip_Flop #(.trigger("rising")) j_k_ff_1 (
    .J(dado[3]), .clk(clk), .K(not_1_out), .Q(out_3[3]));  // open: Qn, preset, en, reset
  not not_1 (not_1_out, dado[3]);
  J_K_Flip_Flop #(.trigger("rising")) j_k_ff_2 (
    .J(dado[2]), .clk(clk), .K(not_2_out), .Q(out_3[2]));  // open: Qn, preset, en, reset
  not not_2 (not_2_out, dado[2]);
  J_K_Flip_Flop #(.trigger("rising")) j_k_ff_3 (
    .J(dado[1]), .clk(clk), .K(not_3_out), .Q(out_3[1]));  // open: Qn, preset, en, reset
  not not_3 (not_3_out, dado[1]);
  J_K_Flip_Flop #(.trigger("rising")) j_k_ff_4 (
    .J(dado[0]), .clk(clk), .K(not_4_out), .Q(out_3[0]));  // open: Qn, preset, en, reset
  not not_4 (not_4_out, dado[0]);

  // Notes on the sheet:
  //   Registrador 4bits
  //   Celso R Franca Jr
endmodule

module Memoria_1x4_JK (
  input  [3:0] Dados___in,
  input  R_W,
  input  cs,
  input  clk,
  output [3:0] Data___out
);

  wire and_1_out, and_2_out, not_1_out;
  wire [3:0] controlled_buffer_2_out, registrador_jk_1_out_3;

  not not_1 (not_1_out, R_W);
  and and_1 (and_1_out, not_1_out, cs);
  and and_2 (and_2_out, cs, R_W);
  assign Data___out = and_2_out ? registrador_jk_1_out_3 : 4'bz;  // Controlled_Buffer controlled_buffer_1
  registrador__JK registrador_jk_1 (.dado(controlled_buffer_2_out), .clk(clk), .out_3(registrador_jk_1_out_3));
  assign controlled_buffer_2_out = and_1_out ? Dados___in : 4'bz;  // Controlled_Buffer controlled_buffer_2

  // Notes on the sheet:
  //   R/W 
  //   1 - leitura
  //   0 - escrita
  //   CS
  //   Memoria 1x4
  //   habilita a gravação
  //   ou a escrita
  //   1 - habilitado
  //   0 - desabilitado
  //   obs:
  //   Celso R Franca Jr
  //   registradores de 4bits 
  //   usando Flip-Flops do tipo JK
endmodule

module Memoria_2x4_JK (
  input  [3:0] dados__in,
  input  R_W,
  input  clk,
  input  cs,
  input  \endereçamento ,
  output [3:0] dados__out
);

  wire demultiplexer_1_out0, demultiplexer_1_out1;

  Demultiplexer #(.select(1), .width(1), .tristate("false")) demultiplexer_1 (
    .out0(demultiplexer_1_out0), .out1(demultiplexer_1_out1), .in(cs), .sel(\endereçamento ));
  Memoria_1x4_JK memoria_1x4_jk_1 (
    .R_W(R_W), .cs(demultiplexer_1_out0), .clk(clk), .Dados___in(dados__in), .Data___out(dados__out));
  Memoria_1x4_JK memoria_1x4_jk_2 (
    .R_W(R_W), .cs(demultiplexer_1_out1), .clk(clk), .Dados___in(dados__in), .Data___out(dados__out));

  // Notes on the sheet:
  //   R/W 
  //   1 - leitura
  //   0 - escrita
  //   CS
  //   Memoria 2x4
  //   habilita a gravação
  //   ou a escrita
  //   1 - habilitado
  //   0 - desabilitado
  //   obs:
  //   Celso R Franca Jr
  //   registradores de 4bits 
  //   usando Flip-Flops do tipo JK
endmodule

module Memoria_1x8_JK (
  input  [7:0] dados__in,
  input  R_W,
  input  cs,
  input  clk,
  output [7:0] dados__out
);

  Memoria_1x4_JK memoria_1x4_jk_1 (
    .R_W(R_W), .cs(cs), .clk(clk), .Dados___in(dados__in[7:4]), .Data___out(dados__out[7:4]));
  Memoria_1x4_JK memoria_1x4_jk_2 (
    .R_W(R_W), .cs(cs), .clk(clk), .Dados___in(dados__in[3:0]), .Data___out(dados__out[3:0]));

  // Notes on the sheet:
  //   R/W 
  //   1 - leitura
  //   0 - escrita
  //   CS
  //   Memoria 1x8
  //   habilita a gravação
  //   ou a escrita
  //   1 - habilitado
  //   0 - desabilitado
  //   obs:
  //   registradores de 4bits 
  //   Celso R Franca Jr
  //   usando Flip-Flops do tipo JK
endmodule

module Memoria_4x8_GT_supercloked (
  input  [7:0] dados__in,
  input  R_W,
  input  clk,
  input  cs,
  input  [1:0] \endereçamento ,
  output [7:0] dados__out
);

  wire demultiplexer_1_out0, demultiplexer_1_out1, demultiplexer_1_out2, demultiplexer_1_out3;

  Demultiplexer #(.select(2), .width(1), .tristate("false")) demultiplexer_1 (
    .out0(demultiplexer_1_out0), .out1(demultiplexer_1_out1), .out2(demultiplexer_1_out2),
    .out3(demultiplexer_1_out3), .in(cs), .sel(\endereçamento ));
  Memoria_1x8_JK memoria_1x8_jk_1 (
    .R_W(R_W), .cs(demultiplexer_1_out0), .clk(clk), .dados__in(dados__in), .dados__out(dados__out));
  Memoria_1x8_JK memoria_1x8_jk_2 (
    .R_W(R_W), .cs(demultiplexer_1_out1), .clk(clk), .dados__in(dados__in), .dados__out(dados__out));
  Memoria_1x8_JK memoria_1x8_jk_3 (
    .R_W(R_W), .cs(demultiplexer_1_out2), .clk(clk), .dados__in(dados__in), .dados__out(dados__out));
  Memoria_1x8_JK memoria_1x8_jk_4 (
    .R_W(R_W), .cs(demultiplexer_1_out3), .clk(clk), .dados__in(dados__in), .dados__out(dados__out));

  // Notes on the sheet:
  //   R/W 
  //   1 - leitura
  //   0 - escrita
  //   CS
  //   Memoria 4x8
  //   habilita a gravação
  //   ou a escrita
  //   1 - habilitado
  //   0 - desabilitado
  //   obs:
  //   registradores de 8bits 
  //   Celso R Franca Jr
  //   usando Flip-Flops do tipo JK
endmodule
