// Logisim project memoria.circ as structural Verilog: 8 circuits, main circuit registrador_4bits
module registrador_4bits (
  input  CLK,
  input  [3:0] Variavel,
  input  [7:0] DATA,
  output [3:0] out_4
);

  wire d_ff_1_q, d_ff_2_q, d_ff_3_q, d_ff_4_q;

  D_Flip_Flop #(.trigger("rising")) d_ff_1 (
    .clk(CLK), .D(Variavel[3]), .Q(d_ff_1_q), .en(DATA[7]));  // open: Qn, preset, reset
  D_Flip_Flop #(.trigger("rising")) d_ff_2 (
    .clk(CLK), .D(Variavel[1]), .Q(d_ff_2_q), .en(DATA[5]));  // open: Qn, preset, reset
  D_Flip_Flop #(.trigger("rising")) d_ff_3 (
    .clk(CLK), .D(Variavel[2]), .Q(d_ff_3_q), .en(DATA[3]));  // open: Qn, preset, reset
  D_Flip_Flop #(.trigger("rising")) d_ff_4 (
    .clk(CLK), .D(Variavel[0]), .Q(d_ff_4_q), .en(DATA[1]));  // open: Qn, preset, reset
  assign out_4[3] = DATA[6] ? d_ff_1_q : 1'bz;  // Controlled_Buffer controlled_buffer_1
  assign out_4[1] = DATA[4] ? d_ff_2_q : 1'bz;  // Controlled_Buffer controlled_buffer_2
  assign out_4[2] = DATA[2] ? d_ff_3_q : 1'bz;  // Controlled_Buffer controlled_buffer_3
  assign out_4[0] = DATA[0] ? d_ff_4_q : 1'bz;  // Controlled_Buffer controlled_buffer_4

  // Notes on the sheet:
  //   Márcia Cibele Martins Carneiro - 404591
  //   Márcia Cibele Martins Carneiro - 404591
  //    Registrador de 4 bits
endmodule

module mem_1x4 (
  input  CLK,
  input  R_W,
  input  ADDR,
  input  [3:0] DADO,
  input  [7:0] DATA,
  output [3:0] out_6
);

  wire and_1_out, not_1_out;
  wire [3:0] registrador_4bits_1_out_4;

  and and_1 (and_1_out, CLK, R_W, ADDR);
  not not_1 (not_1_out, CLK);
  registrador_4bits registrador_4bits_1 (
    .CLK(and_1_out), .Variavel(DADO), .DATA(DATA), .out_4(registrador_4bits_1_out_4));
  Multiplexer #(.select(1), .width(4)) multiplexer_1 (
    .in0(registrador_4bits_1_out_4), .in1(registrador_4bits_1_out_4), .out(out_6), .sel(not_1_out));

  // Notes on the sheet:
  //   Márcia Cibele Martins Carneiro - 404591
  //   Márcia Cibele Martins Carneiro - 404591
  //   Memória RAM 1x4 (1 endereço com 4 bits)
  //   Memória RAM 1x4 (1 endereço com 4 bits)
endmodule

module mem_1x8bits (
  input  CLK,
  input  R_W,
  input  ADR,
  input  [7:0] Variavel,
  input  [15:0] DATA,
  output [7:0] out_6
);

  wire not_1_out;
  wire [3:0] mem_1x4_1_out_6, mem_1x4_2_out_6;

  not not_1 (not_1_out, CLK);
  mem_1x4 mem_1x4_1 (.CLK(CLK), .R_W(R_W), .ADDR(ADR), .DADO(Variavel[3:0]), .DATA(DATA[7:0]), .out_6(mem_1x4_1_out_6));
  mem_1x4 mem_1x4_2 (
    .CLK(CLK), .R_W(R_W), .ADDR(ADR), .DADO(Variavel[7:4]), .DATA(DATA[15:8]), .out_6(mem_1x4_2_out_6));
  Multiplexer #(.select(1), .width(8)) multiplexer_1 (
    .in0({mem_1x4_2_out_6, mem_1x4_1_out_6}), .in1({mem_1x4_2_out_6, mem_1x4_1_out_6}), .out(out_6),
    .sel(not_1_out));

  // Notes on the sheet:
  //   Márcia Cibele Martins Carneiro - 404591
  //   Márcia Cibele Martins Carneiro - 404591
  //   Memória RAM 1x8 usando memórias 1x4 como subcircuitos
  //   Memória RAM 1x8 usando memórias 1x4 como subcircuitos
endmodule

module mem_4x8 (
  input  [1:0] ADDR,
  input  W,
  input  CLK,
  input  [7:0] Variavel,
  input  [15:0] DATA,
  output [7:0] out_6
);

  wire demultiplexer_1_out0, demultiplexer_1_out1, demultiplexer_1_out2, demultiplexer_1_out3;
  wire [7:0] mem_1x8bits_1_out_6, mem_1x8bits_2_out_6, mem_1x8bits_3_out_6, mem_1x8bits_4_out_6;

  Demultiplexer #(.select(2), .width(1), .tristate("false")) demultiplexer_1 (
    .out0(demultiplexer_1_out0), .out1(demultiplexer_1_out1), .out2(demultiplexer_1_out2),
    .out3(demultiplexer_1_out3), .in(W), .sel(ADDR));
  mem_1x8bits mem_1x8bits_1 (
    .CLK(CLK), .R_W(W), .ADR(demultiplexer_1_out3), .Variavel(Variavel), .DATA(DATA),
    .out_6(mem_1x8bits_1_out_6));
  mem_1x8bits mem_1x8bits_2 (
    .CLK(CLK), .R_W(W), .ADR(demultiplexer_1_out2), .Variavel(Variavel), .DATA(DATA),
    .out_6(mem_1x8bits_2_out_6));
  mem_1x8bits mem_1x8bits_3 (
    .CLK(CLK), .R_W(W), .ADR(demultiplexer_1_out1), .Variavel(Variavel), .DATA(DATA),
    .out_6(mem_1x8bits_3_out_6));
  mem_1x8bits mem_1x8bits_4 (
    .CLK(CLK), .R_W(W), .ADR(demultiplexer_1_out0), .Variavel(Variavel), .DATA(DATA),
    .out_6(mem_1x8bits_4_out_6));
  Multiplexer #(.select(2), .width(8)) multiplexer_1 (
    .in0(mem_1x8bits_4_out_6), .in1(mem_1x8bits_3_out_6), .in2(mem_1x8bits_2_out_6),
    .in3(mem_1x8bits_1_out_6), .out(out_6), .sel(ADDR));

  // Notes on the sheet:
  //   Márcia Cibele Martins Carneiro - 404591
  //   Márcia Cibele Martins Carneiro - 404591
  //   Memória RAM 4x8 usando memórias 1x8 como subcircuitos
  //   Memória RAM 4x8 usando memórias 1x8 como subcircuitos
endmodule

module mem_1x4_JK (
  input  [3:0] DADO,
  input  R_W,
  input  ADDR,
  input  CLK,
  output [3:0] out_5
);

  wire and_1_out, not_1_out, not_2_out, not_3_out, not_4_out, not_5_out;
  wire [3:0] j_k_ff_1_q;

  and and_1 (and_1_out, R_W, ADDR, CLK);
  not not_1 (not_1_out, CLK);
  not not_2 (not_2_out, DADO[0]);
  not not_3 (not_3_out, DADO[1]);
  not not_4 (not_4_out, DADO[2]);
  not not_5 (not_5_out, DADO[3]);
  J_K_Flip_Flop #(.trigger("rising")) j_k_ff_1 (
    .J(DADO[0]), .clk(and_1_out), .K(not_2_out), .Q(j_k_ff_1_q[0]));  // open: Qn, preset, en, reset
  J_K_Flip_Flop #(.trigger("rising")) j_k_ff_2 (
    .J(DADO[1]), .clk(and_1_out), .K(not_3_out), .Q(j_k_ff_1_q[1]));  // open: Qn, preset, en, reset
  J_K_Flip_Flop #(.trigger("rising")) j_k_ff_3 (
    .J(DADO[2]), .clk(and_1_out), .K(not_4_out), .Q(j_k_ff_1_q[2]));  // open: Qn, preset, en, reset
  J_K_Flip_Flop #(.trigger("rising")) j_k_ff_4 (
    .J(DADO[3]), .clk(and_1_out), .K(not_5_out), .Q(j_k_ff_1_q[3]));  // open: Qn, preset, en, reset
  assign out_5 = not_1_out ? j_k_ff_1_q : 4'bz;  // Controlled_Buffer controlled_buffer_1

  // Notes on the sheet:
  //   Márcia Cibele Martins Carneiro - 404591
  //   Márcia Cibele Martins Carneiro - 404591
  //   aqui já são os dois juntos, pois no de 4x8 já está 'contido' o 2x4
  //   Memória RAM 1x4 usando flip-flops do tipo JK como registradores de dados
  //   Memória RAM 1x4 usando flip-flops do tipo JK como registradores de dados
endmodule

module mem_2x4_JK (
  input  [3:0] DADO,
  input  R_W,
  input  ADDR,
  input  CLK,
  output [3:0] out_5
);

  wire demultiplexer_1_out0, demultiplexer_1_out1;
  wire [3:0] mem_1x4_jk_1_out_5, mem_1x4_jk_2_out_5;

  Demultiplexer #(.select(1), .width(1), .tristate("false")) demultiplexer_1 (
    .out0(demultiplexer_1_out0), .out1(demultiplexer_1_out1), .in(1'b1), .sel(ADDR));
  mem_1x4_JK mem_1x4_jk_1 (.DADO(DADO), .R_W(R_W), .ADDR(demultiplexer_1_out0), .CLK(CLK), .out_5(mem_1x4_jk_1_out_5));
  mem_1x4_JK mem_1x4_jk_2 (.DADO(DADO), .R_W(R_W), .ADDR(demultiplexer_1_out1), .CLK(CLK), .out_5(mem_1x4_jk_2_out_5));
  Multiplexer #(.select(1), .width(4)) multiplexer_1 (
    .in0(mem_1x4_jk_1_out_5), .in1(mem_1x4_jk_2_out_5), .out(out_5), .sel(ADDR));

  // Notes on the sheet:
  //   Márcia Cibele Martins Carneiro - 404591
  //   Márcia Cibele Martins Carneiro - 404591
  //   Memória RAM 2x4 usando flip-flops do tipo JK como registradores de dados
  //   Memória RAM 2x4 usando flip-flops do tipo JK como registradores de dados
endmodule

module mem_4x8_JK (
  input  R_W,
  input  [1:0] ADDR,
  input  CLK,
  input  [7:0] DADO,
  output [7:0] out_5
);

  wire decoder_1_out0, decoder_1_out1, decoder_1_out2, decoder_1_out3;
  wire [7:0] mem_1x8_jk_1_out_5, mem_1x8_jk_2_out_5, mem_1x8_jk_3_out_5, mem_1x8_jk_4_out_5;

  Decoder #(.select(2), .tristate("false")) decoder_1 (
    .out0(decoder_1_out0), .out1(decoder_1_out1), .out2(decoder_1_out2), .out3(decoder_1_out3), .sel(ADDR));
  mem_1x8_JK mem_1x8_jk_1 (.R_W(R_W), .ADDR(decoder_1_out0), .CLK(CLK), .DADO(DADO), .out_5(mem_1x8_jk_1_out_5));
  mem_1x8_JK mem_1x8_jk_2 (.R_W(R_W), .ADDR(decoder_1_out1), .CLK(CLK), .DADO(DADO), .out_5(mem_1x8_jk_2_out_5));
  mem_1x8_JK mem_1x8_jk_3 (.R_W(R_W), .ADDR(decoder_1_out2), .CLK(CLK), .DADO(DADO), .out_5(mem_1x8_jk_3_out_5));
  mem_1x8_JK mem_1x8_jk_4 (.R_W(R_W), .ADDR(decoder_1_out3), .CLK(CLK), .DADO(DADO), .out_5(mem_1x8_jk_4_out_5));
  Multiplexer #(.select(2), .width(8)) multiplexer_1 (
    .in0(mem_1x8_jk_1_out_5), .in1(mem_1x8_jk_2_out_5), .in2(mem_1x8_jk_3_out_5), .in3(mem_1x8_jk_4_out_5),
    .out(out_5), .sel(ADDR));

  // Notes on the sheet:
  //   Márcia Cibele Martins Carneiro - 404591
  //   Márcia Cibele Martins Carneiro - 404591
  //   Memória RAM 4x8 usando flip-flops do tipo JK como registradores de dados
  //   Memória RAM 4x8 usando flip-flops do tipo JK como registradores de dados
endmodule

module mem_1x8_JK (
  input  R_W,
  input  ADDR,
  input  CLK,
  input  [7:0] DADO,
  output [7:0] out_5
);

  mem_1x4_JK mem_1x4_jk_1 (.DADO(DADO[3:0]), .R_W(R_W), .ADDR(ADDR), .CLK(CLK), .out_5(out_5[3:0]));
  mem_1x4_JK mem_1x4_jk_2 (.DADO(DADO[7:4]), .R_W(R_W), .ADDR(ADDR), .CLK(CLK), .out_5(out_5[7:4]));

  // Notes on the sheet:
  //   Márcia Cibele Martins Carneiro - 404591
  //   Márcia Cibele Martins Carneiro - 404591
  //   Memória RAM 1x8 usando flip-flops do tipo JK como registradores de dados
  //   Memória RAM 1x8 usando flip-flops do tipo JK como registradores de dados
endmodule
