// Logisim project G14E2.circ as structural Verilog: 3 circuits, main circuit RAM 1x4
module RAM_1x4 (
  input  [3:0] \input ,
  input  R_W,
  input  CLK,
  input  CS,
  input  CLR,
  output [3:0] \outpút 
);

  wire and_1_out, and_2_out, not_1_out, not_2_out, not_3_out;
  wire [3:0] controlled_buffer_1_out, reg_1_output;

  not not_1 (not_1_out, R_W);
  and and_1 (and_1_out, not_1_out, not_2_out);
  not not_2 (not_2_out, CS);
  not not_3 (not_3_out, CS);
  and and_2 (and_2_out, not_3_out, R_W);
  assign controlled_buffer_1_out = and_1_out ? \input  : 4'bz;  // Controlled_Buffer controlled_buffer_1
  \reg  reg_1 (.\input (controlled_buffer_1_out), .CLK(CLK), .CLR(CLR), .\output (reg_1_output));
  assign \outpút  = and_2_out ? reg_1_output : 4'bz;  // Controlled_Buffer controlled_buffer_2

  // Notes on the sheet:
  //   Guia 14_02 -  RAM 1x4
  //   Nome: Alan Diniz Nogueira Machado
  //   Matrícula:405782
endmodule

module \reg  (
  input  [3:0] \input ,
  input  CLK,
  input  CLR,
  output [3:0] \output 
);

  D_Flip_Flop #(.trigger("rising")) d_ff_1 (
    .clk(CLK), .D(\input [3]), .Q(\output [3]), .reset(CLR));  // open: Qn, preset, en
  D_Flip_Flop #(.trigger("rising")) d_ff_2 (
    .clk(CLK), .D(\input [2]), .Q(\output [2]), .reset(CLR));  // open: Qn, preset, en
  D_Flip_Flop #(.trigger("rising")) d_ff_3 (
    .clk(CLK), .D(\input [1]), .Q(\output [1]), .reset(CLR));  // open: Qn, preset, en
  D_Flip_Flop #(.trigger("rising")) d_ff_4 (
    .clk(CLK), .D(\input [0]), .Q(\output [0]), .reset(CLR));  // open: Qn, preset, en

  // Notes on the sheet:
  //   Nome: Alan Diniz Nogueira Machado
  //   Matrícula:405782
  //   Guia 14_02 -  Registrador de 4bits com flip-flops D
endmodule

module RAM_1x8 (
  input  [7:0] \input ,
  input  R_W,
  input  CS,
  input  CLK,
  input  CLR,
  output [7:0] \output 
);

  RAM_1x4 ram_1x4_1 (.R_W(R_W), .CLK(CLK), .CS(CS), .CLR(CLR), .\input (\input [7:4]), .\outpút (\output [7:4]));
  RAM_1x4 ram_1x4_2 (.R_W(R_W), .CLK(CLK), .CS(CS), .CLR(CLR), .\input (\input [3:0]), .\outpút (\output [3:0]));

  // Notes on the sheet:
  //   Guia 14_02 -  RAM 1x8
  //   Nome: Alan Diniz Nogueira Machado
  //   Matrícula:405782
endmodule
