// Logisim project G14E5.circ as structural Verilog: 4 circuits, main circuit RAM 1x4
module RAM_1x4 (
  input  [3:0] \input ,
  input  R_W,
  input  CLK,
  input  CS,
  input  CLR,
  output [3:0] \outpút 
);

  wire and_1_out, and_2_out, not_1_out, not_2_out, not_3_out;
  wire [3:0] controlled_buffer_1_out, reg_1_output;

  not not_1 (not_1_out, R_W);
  and and_1 (and_1_out, not_1_out, not_2_out);
  not not_2 (not_2_out, CS);
  not not_3 (not_3_out, CS);
  and and_2 (and_2_out, not_3_out, R_W);
  assign controlled_buffer_1_out = and_1_out ? \input  : 4'bz;  // Controlled_Buffer controlled_buffer_1
  \reg  reg_1 (.\input (controlled_buffer_1_out), .CLK(CLK), .CLR(CLR), .\output (reg_1_output));
  assign \outpút  = and_2_out ? reg_1_output : 4'bz;  // Controlled_Buffer controlled_buffer_2

  // Notes on the sheet:
  //   Guia 14_05 -  RAM 1x4
  //   Nome: Alan Diniz Nogueira Machado
  //   Matrícula:405782
endmodule

module \reg  (
  input  [3:0] \input ,
  input  CLK,
  input  CLR,
  output [3:0] \output 
);

  wire not_1_out, not_2_out, not_3_out, not_4_out;

  J_K_Flip_Flop #(.trigger("rising")) j_k_ff_1 (
    .J(\input [3]), .clk(CLK), .K(not_1_out), .Q(\output [3]), .reset(CLR));  // open: Qn, preset, en
  not not_1 (not_1_out, \input [3]);
  J_K_Flip_Flop #(.trigger("rising")) j_k_ff_2 (
    .J(\input [2]), .clk(CLK), .K(not_2_out), .Q(\output [2]), .reset(CLR));  // open: Qn, preset, en
  not not_2 (not_2_out, \input [2]);
  J_K_Flip_Flop #(.trigger("rising")) j_k_ff_3 (
    .J(\input [1]), .clk(CLK), .K(not_3_out), .Q(\output [1]), .reset(CLR));  // open: Qn, preset, en
  not not_3 (not_3_out, \input [1]);
  J_K_Flip_Flop #(.trigger("rising")) j_k_ff_4 (
    .J(\input [0]), .clk(CLK), .K(not_4_out), .Q(\output [0]), .reset(CLR));  // open: Qn, preset, en
  not not_4 (not_4_out, \input [0]);

  // Notes on the sheet:
  //   Nome: Alan Diniz Nogueira Machado
  //   Matrícula:405782
  //   Guia 14_05 -  Registrador de 4bits com flip-flops JK
endmodule

module RAM_1x8 (
  input  [7:0] \input ,
  input  R_W,
  input  CS,
  input  CLK,
  input  CLR,
  output [7:0] \output 
);

  RAM_1x4 ram_1x4_1 (.R_W(R_W), .CLK(CLK), .CS(CS), .CLR(CLR), .\input (\input [7:4]), .\outpút (\output [7:4]));
  RAM_1x4 ram_1x4_2 (.R_W(R_W), .CLK(CLK), .CS(CS), .CLR(CLR), .\input (\input [3:0]), .\outpút (\output [3:0]));

  // Notes on the sheet:
  //   Guia 14_05 -  RAM 1x8
  //   Nome: Alan Diniz Nogueira Machado
  //   Matrícula:405782
endmodule

module RAM_4x8 (
  input  R_W,
  input  [7:0] \input ,
  input  [1:0] adress,
  input  CLR,
  output [7:0] \output 
);

  wire clock_1_out, decoder_1_out0, decoder_1_out1, decoder_1_out2, decoder_1_out3, not_1_out, not_2_out,
       not_3_out, not_4_out;

  Clock #(.highDuration(1), .lowDuration(1)) clock_1 (.out(clock_1_out));
  not not_1 (not_1_out, decoder_1_out0);
  not not_2 (not_2_out, decoder_1_out1);
  not not_3 (not_3_out, decoder_1_out2);
  not not_4 (not_4_out, decoder_1_out3);
  Decoder #(.select(2), .tristate("false")) decoder_1 (
    .out0(decoder_1_out0), .out1(decoder_1_out1), .out2(decoder_1_out2), .out3(decoder_1_out3), .sel(adress));
  RAM_1x8 ram_1x8_1 (.R_W(R_W), .CS(not_1_out), .CLK(clock_1_out), .CLR(CLR), .\input (\input ), .\output (\output ));
  RAM_1x8 ram_1x8_2 (.R_W(R_W), .CS(not_2_out), .CLK(clock_1_out), .CLR(CLR), .\input (\input ), .\output (\output ));
  RAM_1x8 ram_1x8_3 (.R_W(R_W), .CS(not_3_out), .CLK(clock_1_out), .CLR(CLR), .\input (\input ), .\output (\output ));
  RAM_1x8 ram_1x8_4 (.R_W(R_W), .CS(not_4_out), .CLK(clock_1_out), .CLR(CLR), .\input (\input ), .\output (\output ));

  // Notes on the sheet:
  //   Guia 14_05 -  RAM 4x8
  //   Nome: Alan Diniz Nogueira Machado
  //   Matrícula:405782
endmodule
