// Logisim project Guia_14.circ as structural Verilog
module RAM_1x4 (
  input  Clock,
  input  Clear,
  input  [3:0] Dados,
  input  Address,
  input  R_W,
  output [3:0] out_6
);

  wire and_1_out, not_1_out, not_2_out;
  wire [3:0] controlled_buffer_1_out, d_ff_4_q;

  not not_1 (not_1_out, Clock);
  assign controlled_buffer_1_out = and_1_out ? Dados : 4'bz;  // Controlled_Buffer controlled_buffer_1
  and and_1 (and_1_out, not_1_out, Address, R_W);
  not not_2 (not_2_out, R_W);
  D_Flip_Flop #(.trigger("rising")) d_ff_1 (
    .clk(Clock), .D(controlled_buffer_1_out[3]), .Q(d_ff_4_q[3]), .en(Address), .reset(Clear));  // open: Qn, preset
  D_Flip_Flop #(.trigger("rising")) d_ff_2 (
    .clk(Clock), .D(controlled_buffer_1_out[2]), .Q(d_ff_4_q[2]), .en(Address), .reset(Clear));  // open: Qn, preset
  D_Flip_Flop #(.trigger("rising")) d_ff_3 (
    .clk(Clock), .D(controlled_buffer_1_out[1]), .Q(d_ff_4_q[1]), .en(Address), .reset(Clear));  // open: Qn, preset
  D_Flip_Flop #(.trigger("rising")) d_ff_4 (
    .clk(Clock), .D(controlled_buffer_1_out[0]), .Q(d_ff_4_q[0]), .en(Address), .reset(Clear));  // open: Qn, preset
  assign out_6 = not_2_out ? d_ff_4_q : 4'bz;  // Controlled_Buffer controlled_buffer_2
endmodule

module RAM_1x8 (
  input  Clock,
  input  [7:0] Dados,
  input  Clear,
  input  R_W,
  input  Address,
  output [7:0] out_6
);

  RAM_1x4 ram_1x4_1 (
    .Clock(Clock), .Clear(Clear), .Dados(Dados[3:0]), .Address(Address), .R_W(R_W), .out_6(out_6[3:0]));
  RAM_1x4 ram_1x4_2 (
    .Clock(Clock), .Clear(Clear), .Dados(Dados[7:4]), .Address(Address), .R_W(R_W), .out_6(out_6[7:4]));
endmodule

module RAM_4x8 (
  input  Clock,
  input  [7:0] Dados,
  input  Clear,
  input  R_W,
  input  [1:0] Address,
  output [7:0] out_6
);

  wire demultiplexer_1_out0, demultiplexer_1_out1, demultiplexer_1_out2, demultiplexer_1_out3;
  wire [7:0] ram_1x8_1_out_6, ram_1x8_2_out_6, ram_1x8_3_out_6, ram_1x8_4_out_6;

  Demultiplexer #(.select(2), .width(1), .tristate("false")) demultiplexer_1 (
    .out0(demultiplexer_1_out0), .out1(demultiplexer_1_out1), .out2(demultiplexer_1_out2),
    .out3(demultiplexer_1_out3), .in(1'b1), .sel(Address));
  RAM_1x8 ram_1x8_1 (
    .Clock(Clock), .Dados(Dados), .Clear(Clear), .R_W(R_W), .Address(demultiplexer_1_out0),
    .out_6(ram_1x8_1_out_6));
  RAM_1x8 ram_1x8_2 (
    .Clock(Clock), .Dados(Dados), .Clear(Clear), .R_W(R_W), .Address(demultiplexer_1_out1),
    .out_6(ram_1x8_2_out_6));
  Multiplexer #(.select(2), .width(8)) multiplexer_1 (
    .in0(ram_1x8_1_out_6), .in1(ram_1x8_2_out_6), .in2(ram_1x8_3_out_6), .in3(ram_1x8_4_out_6), .out(out_6),
    .sel(Address));
  RAM_1x8 ram_1x8_3 (
    .Clock(Clock), .Dados(Dados), .Clear(Clear), .R_W(R_W), .Address(demultiplexer_1_out2),
    .out_6(ram_1x8_3_out_6));
  RAM_1x8 ram_1x8_4 (
    .Clock(Clock), .Dados(Dados), .Clear(Clear), .R_W(R_W), .Address(demultiplexer_1_out3),
    .out_6(ram_1x8_4_out_6));
endmodule
