// Logisim project Guia14.circ as structural Verilog
module RAM_1x4 (
  input  ADDR,
  input  CLK,
  input  R_W,
  input  [3:0] DATA,
  input  CLR,
  output [3:0] Saida
);

  wire and_1_out;
  wire [3:0] d_ff_1_q;

  and and_1 (and_1_out, ADDR, CLK, R_W);
  D_Flip_Flop #(.trigger("rising")) d_ff_1 (
    .clk(and_1_out), .D(DATA[0]), .Q(d_ff_1_q[0]), .reset(CLR));  // open: Qn, preset, en
  D_Flip_Flop #(.trigger("rising")) d_ff_2 (
    .clk(and_1_out), .D(DATA[1]), .Q(d_ff_1_q[1]), .reset(CLR));  // open: Qn, preset, en
  D_Flip_Flop #(.trigger("rising")) d_ff_3 (
    .clk(and_1_out), .D(DATA[2]), .Q(d_ff_1_q[2]), .reset(CLR));  // open: Qn, preset, en
  D_Flip_Flop #(.trigger("rising")) d_ff_4 (
    .clk(and_1_out), .D(DATA[3]), .Q(d_ff_1_q[3]), .reset(CLR));  // open: Qn, preset, en
  assign Saida = ADDR ? d_ff_1_q : 4'bz;  // Controlled_Buffer controlled_buffer_1

  // Notes on the sheet:
  //   Nome: Gustavo Guimarães
  //   Matricula: 405804
endmodule

module RAM_1x8 (
  input  ADDR,
  input  CLK,
  input  R_W,
  input  [7:0] DATA,
  input  CLR,
  output [7:0] Saida
);

  RAM_1x4 ram_1x4_1 (.ADDR(ADDR), .CLK(CLK), .R_W(R_W), .DATA(DATA[3:0]), .CLR(CLR), .Saida(Saida[3:0]));
  RAM_1x4 ram_1x4_2 (.ADDR(ADDR), .CLK(CLK), .R_W(R_W), .DATA(DATA[7:4]), .CLR(CLR), .Saida(Saida[7:4]));

  // Notes on the sheet:
  //   Nome: Gustavo Guimarães
  //   Matricula: 405804
endmodule

module RAM_4x8 (
  input  R_W,
  input  CLK,
  input  [1:0] ADDR,
  input  [7:0] DATA,
  input  CLR,
  output [7:0] Saida
);

  wire demultiplexer_1_out0, demultiplexer_1_out1, demultiplexer_1_out2, demultiplexer_1_out3;
  wire [7:0] ram_1x8_1_saida, ram_1x8_2_saida, ram_1x8_3_saida, ram_1x8_4_saida;

  Demultiplexer #(.select(2), .width(1), .tristate("false")) demultiplexer_1 (
    .out0(demultiplexer_1_out0), .out1(demultiplexer_1_out1), .out2(demultiplexer_1_out2),
    .out3(demultiplexer_1_out3), .in(CLK), .sel(ADDR));
  RAM_1x8 ram_1x8_1 (
    .ADDR(demultiplexer_1_out0), .CLK(CLK), .R_W(R_W), .DATA(DATA), .CLR(CLR), .Saida(ram_1x8_1_saida));
  RAM_1x8 ram_1x8_2 (
    .ADDR(demultiplexer_1_out1), .CLK(CLK), .R_W(R_W), .DATA(DATA), .CLR(CLR), .Saida(ram_1x8_2_saida));
  RAM_1x8 ram_1x8_3 (
    .ADDR(demultiplexer_1_out2), .CLK(CLK), .R_W(R_W), .DATA(DATA), .CLR(CLR), .Saida(ram_1x8_3_saida));
  RAM_1x8 ram_1x8_4 (
    .ADDR(demultiplexer_1_out3), .CLK(CLK), .R_W(R_W), .DATA(DATA), .CLR(CLR), .Saida(ram_1x8_4_saida));
  Multiplexer #(.select(2), .width(8)) multiplexer_1 (
    .in0(ram_1x8_1_saida), .in1(ram_1x8_2_saida), .in2(ram_1x8_3_saida), .in3(ram_1x8_4_saida), .out(Saida),
    .sel(ADDR));

  // Notes on the sheet:
  //   Nome: Gustavo Guimarães
  //   Matricula: 405804
endmodule
