// Logisim project guia_14.circ as structural Verilog: 3 circuits, main circuit ex_01
module ex_01 (
  input  ADDR,
  input  CLK,
  input  R_W,
  input  [3:0] DATA,
  input  CLR,
  output [3:0] OUT
);

  wire and_1_out;
  wire [3:0] d_ff_1_q;

  and and_1 (and_1_out, ADDR, CLK, R_W);
  D_Flip_Flop #(.trigger("rising")) d_ff_1 (
    .clk(and_1_out), .D(DATA[0]), .Q(d_ff_1_q[0]), .reset(CLR));  // open: Qn, preset, en
  D_Flip_Flop #(.trigger("rising")) d_ff_2 (
    .clk(and_1_out), .D(DATA[1]), .Q(d_ff_1_q[1]), .reset(CLR));  // open: Qn, preset, en
  D_Flip_Flop #(.trigger("rising")) d_ff_3 (
    .clk(and_1_out), .D(DATA[2]), .Q(d_ff_1_q[2]), .reset(CLR));  // open: Qn, preset, en
  D_Flip_Flop #(.trigger("rising")) d_ff_4 (
    .clk(and_1_out), .D(DATA[3]), .Q(d_ff_1_q[3]), .reset(CLR));  // open: Qn, preset, en
  assign OUT = ADDR ? d_ff_1_q : 4'bz;  // Controlled_Buffer controlled_buffer_1

  // Notes on the sheet:
  //   José Erimá Fernandes Júnior 405807
endmodule

module ex_02 (
  input  ADDR,
  input  CLK,
  input  R_W,
  input  CLR,
  input  [7:0] DATA,
  output [7:0] out_6
);

  ex_01 ex_01_1 (.ADDR(ADDR), .CLK(CLK), .R_W(R_W), .DATA(DATA[3:0]), .CLR(CLR), .OUT(out_6[7:4]));
  ex_01 ex_01_2 (.ADDR(ADDR), .CLK(CLK), .R_W(R_W), .DATA(DATA[7:4]), .CLR(CLR), .OUT(out_6[3:0]));
endmodule

module ex_03 (
  input  R_W,
  input  CLK,
  input  [1:0] ADDR,
  input  in_4,
  input  [7:0] DATA,
  output [7:0] out_6
);

  wire demultiplexer_1_out0, demultiplexer_1_out1, demultiplexer_1_out2, demultiplexer_1_out3;
  wire [7:0] ex_02_1_out_6, ex_02_2_out_6, ex_02_3_out_6, ex_02_4_out_6;

  Demultiplexer #(.select(2), .width(1), .tristate("false")) demultiplexer_1 (
    .out0(demultiplexer_1_out0), .out1(demultiplexer_1_out1), .out2(demultiplexer_1_out2),
    .out3(demultiplexer_1_out3), .in(CLK), .sel(ADDR));
  ex_02 ex_02_1 (.ADDR(demultiplexer_1_out0), .CLK(CLK), .R_W(R_W), .CLR(in_4), .DATA(DATA), .out_6(ex_02_1_out_6));
  ex_02 ex_02_2 (.ADDR(demultiplexer_1_out1), .CLK(CLK), .R_W(R_W), .CLR(in_4), .DATA(DATA), .out_6(ex_02_2_out_6));
  Multiplexer #(.select(2), .width(8)) multiplexer_1 (
    .in0(ex_02_1_out_6), .in1(ex_02_2_out_6), .in2(ex_02_3_out_6), .in3(ex_02_4_out_6), .out(out_6),
    .sel(ADDR));
  ex_02 ex_02_3 (.ADDR(demultiplexer_1_out2), .CLK(CLK), .R_W(R_W), .CLR(in_4), .DATA(DATA), .out_6(ex_02_3_out_6));
  ex_02 ex_02_4 (.ADDR(demultiplexer_1_out3), .CLK(CLK), .R_W(R_W), .CLR(in_4), .DATA(DATA), .out_6(ex_02_4_out_6));
endmodule
