// Logisim project Guia14.circ as structural Verilog: 4 circuits, main circuit Guia1401
module Guia1401 (
  input  ADD,
  input  CLK,
  input  R_W,
  input  CLEAR,
  input  [3:0] DADO,
  output OUTPUT
);

  wire and_1_out, d_ff_1_q, d_ff_2_q, d_ff_3_q, d_ff_4_q;

  and and_1 (and_1_out, ADD, CLK, R_W);
  D_Flip_Flop #(.trigger("rising")) d_ff_1 (
    .clk(and_1_out), .D(DADO[0]), .Q(d_ff_1_q), .reset(CLEAR));  // open: Qn, preset, en
  D_Flip_Flop #(.trigger("rising")) d_ff_2 (
    .clk(and_1_out), .D(DADO[1]), .Q(d_ff_2_q), .reset(CLEAR));  // open: Qn, preset, en
  D_Flip_Flop #(.trigger("rising")) d_ff_3 (
    .clk(and_1_out), .D(DADO[2]), .Q(d_ff_3_q), .reset(CLEAR));  // open: Qn, preset, en
  D_Flip_Flop #(.trigger("rising")) d_ff_4 (
    .clk(and_1_out), .D(DADO[3]), .Q(d_ff_4_q), .reset(CLEAR));  // open: Qn, preset, en
  and and_2 (OUTPUT, d_ff_4_q, d_ff_3_q, d_ff_2_q, d_ff_1_q);

  // Notes on the sheet:
  //   Luiz Felipe Fonseca - 405817
endmodule

module Guia1402 (
  input  in_1,
  input  in_2,
  input  CLK,
  input  CLEAR,
  input  [7:0] DADO,
  output OUTPUT
);

  wire guia1401_1_output, guia1401_2_output;

  Guia1401 guia1401_1 (.ADD(in_1), .CLK(in_2), .R_W(CLK), .CLEAR(CLEAR), .DADO(DADO[3:0]), .OUTPUT(guia1401_1_output));
  Guia1401 guia1401_2 (.ADD(in_1), .CLK(in_2), .R_W(CLK), .CLEAR(CLEAR), .DADO(DADO[7:4]), .OUTPUT(guia1401_2_output));
  and and_1 (OUTPUT, guia1401_2_output, guia1401_1_output);

  // Notes on the sheet:
  //   Luiz Felipe Fonseca - 405817
endmodule

module Guia1403 (
  input  [7:0] DADO,
  input  CLK,
  input  R_W,
  input  [1:0] END,
  input  CLEAR,
  output OUTPUT
);

  wire and_1_out, demultiplexer_1_out0, demultiplexer_1_out1, demultiplexer_1_out2, demultiplexer_1_out3,
       guia1402_1_output, guia1402_2_output, guia1402_3_output, guia1402_4_output;

  and and_1 (and_1_out, CLK, R_W);
  Demultiplexer #(.select(2), .width(1), .tristate("false")) demultiplexer_1 (
    .out0(demultiplexer_1_out0), .out1(demultiplexer_1_out1), .out2(demultiplexer_1_out2),
    .out3(demultiplexer_1_out3), .in(and_1_out), .sel(END));
  Guia1402 guia1402_1 (
    .in_1(demultiplexer_1_out0), .in_2(demultiplexer_1_out0), .CLK(demultiplexer_1_out0), .CLEAR(CLEAR),
    .DADO(DADO), .OUTPUT(guia1402_1_output));
  Guia1402 guia1402_2 (
    .in_1(demultiplexer_1_out1), .in_2(demultiplexer_1_out1), .CLK(demultiplexer_1_out1), .CLEAR(CLEAR),
    .DADO(DADO), .OUTPUT(guia1402_2_output));
  Guia1402 guia1402_3 (
    .in_1(demultiplexer_1_out2), .in_2(demultiplexer_1_out2), .CLK(demultiplexer_1_out2), .CLEAR(CLEAR),
    .DADO(DADO), .OUTPUT(guia1402_3_output));
  Guia1402 guia1402_4 (
    .in_1(demultiplexer_1_out3), .in_2(demultiplexer_1_out3), .CLK(demultiplexer_1_out3), .CLEAR(CLEAR),
    .DADO(DADO), .OUTPUT(guia1402_4_output));
  buf and_2 (OUTPUT, guia1402_1_output);  // AND_Gate

  // Notes on the sheet:
  //   Luiz Felipe Fonseca - 405817
endmodule

module Guia1404 (
  input  [7:0] DADO,
  input  CLK,
  input  R_W,
  input  [2:0] END,
  input  CLEAR,
  output OUTPUT
);

  wire and_1_out, demultiplexer_1_out0, demultiplexer_1_out1, demultiplexer_1_out2, demultiplexer_1_out3,
       demultiplexer_1_out4, demultiplexer_1_out5, demultiplexer_1_out6, demultiplexer_1_out7, j_k_ff_1_q,
       j_k_ff_2_q, j_k_ff_3_q, j_k_ff_4_q, j_k_ff_5_q, j_k_ff_6_q, j_k_ff_7_q, j_k_ff_8_q, not_1_out,
       not_2_out, not_3_out, not_4_out, not_5_out, not_6_out, not_7_out, not_8_out;

  Demultiplexer #(.select(3), .width(1), .tristate("false")) demultiplexer_1 (
    .out0(demultiplexer_1_out0), .out1(demultiplexer_1_out1), .out2(demultiplexer_1_out2),
    .out3(demultiplexer_1_out3), .out4(demultiplexer_1_out4), .out5(demultiplexer_1_out5),
    .out6(demultiplexer_1_out6), .out7(demultiplexer_1_out7), .in(and_1_out), .sel(END));
  and and_1 (and_1_out, CLK, R_W);
  not not_1 (not_1_out, DADO[7]);
  not not_2 (not_2_out, DADO[3]);
  J_K_Flip_Flop #(.trigger("rising")) j_k_ff_1 (
    .J(DADO[7]), .clk(demultiplexer_1_out0), .K(not_1_out), .Q(j_k_ff_1_q), .reset(CLEAR));  // open: Qn, preset, en
  J_K_Flip_Flop #(.trigger("rising")) j_k_ff_2 (
    .J(DADO[3]), .clk(demultiplexer_1_out4), .K(not_2_out), .Q(j_k_ff_2_q), .reset(CLEAR));  // open: Qn, preset, en
  J_K_Flip_Flop #(.trigger("rising")) j_k_ff_3 (
    .J(DADO[6]), .clk(demultiplexer_1_out1), .K(not_3_out), .Q(j_k_ff_3_q), .reset(CLEAR));  // open: Qn, preset, en
  not not_3 (not_3_out, DADO[6]);
  J_K_Flip_Flop #(.trigger("rising")) j_k_ff_4 (
    .J(DADO[2]), .clk(demultiplexer_1_out5), .K(not_4_out), .Q(j_k_ff_4_q), .reset(CLEAR));  // open: Qn, preset, en
  not not_4 (not_4_out, DADO[2]);
  not not_5 (not_5_out, DADO[1]);
  J_K_Flip_Flop #(.trigger("rising")) j_k_ff_5 (
    .J(DADO[5]), .clk(demultiplexer_1_out2), .K(not_6_out), .Q(j_k_ff_5_q), .reset(CLEAR));  // open: Qn, preset, en
  not not_6 (not_6_out, DADO[5]);
  J_K_Flip_Flop #(.trigger("rising")) j_k_ff_6 (
    .J(DADO[1]), .clk(demultiplexer_1_out6), .K(not_5_out), .Q(j_k_ff_6_q), .reset(CLEAR));  // open: Qn, preset, en
  not not_7 (not_7_out, DADO[4]);
  not not_8 (not_8_out, DADO[0]);
  J_K_Flip_Flop #(.trigger("rising")) j_k_ff_7 (
    .J(DADO[4]), .clk(demultiplexer_1_out3), .K(not_7_out), .Q(j_k_ff_7_q), .reset(CLEAR));  // open: Qn, preset, en
  J_K_Flip_Flop #(.trigger("rising")) j_k_ff_8 (
    .J(DADO[0]), .clk(demultiplexer_1_out7), .K(not_8_out), .Q(j_k_ff_8_q), .reset(CLEAR));  // open: Qn, preset, en
  and and_2 (OUTPUT, j_k_ff_7_q, j_k_ff_5_q, j_k_ff_3_q, j_k_ff_1_q, j_k_ff_8_q, j_k_ff_6_q, j_k_ff_4_q, j_k_ff_2_q);

  // Notes on the sheet:
  //   Luiz Felipe Fonseca - 405817
endmodule
