// Logisim project memoria.circ as structural Verilog
module ram_1x4 (
  input  clock,
  input  write,
  input  address,
  input  [3:0] data,
  output [3:0] s
);

  wire and_1_out, not_1_out;
  wire [3:0] d_ff_1_q;

  and and_1 (and_1_out, clock, write, address);
  D_Flip_Flop #(.trigger("rising")) d_ff_1 (
    .clk(and_1_out), .D(data[0]), .Q(d_ff_1_q[0]));  // open: Qn, preset, en, reset
  D_Flip_Flop #(.trigger("rising")) d_ff_2 (
    .clk(and_1_out), .D(data[1]), .Q(d_ff_1_q[1]));  // open: Qn, preset, en, reset
  D_Flip_Flop #(.trigger("rising")) d_ff_3 (
    .clk(and_1_out), .D(data[2]), .Q(d_ff_1_q[2]));  // open: Qn, preset, en, reset
  D_Flip_Flop #(.trigger("rising")) d_ff_4 (
    .clk(and_1_out), .D(data[3]), .Q(d_ff_1_q[3]));  // open: Qn, preset, en, reset
  not not_1 (not_1_out, clock);
  assign s = not_1_out ? d_ff_1_q : 4'bz;  // Controlled_Buffer controlled_buffer_1
endmodule

module ram_1x8 (
  input  clock,
  input  write,
  input  address,
  input  [7:0] data,
  output [7:0] s
);

  ram_1x4 ram_1x4_1 (.clock(clock), .write(write), .address(address), .data(data[3:0]), .s(s[3:0]));
  ram_1x4 ram_1x4_2 (.clock(clock), .write(write), .address(address), .data(data[7:4]), .s(s[7:4]));

  // Notes on the sheet:
  //   RAM 1x4
  //   RAM 1x4
endmodule

module ram_4x8 (
  input  clock,
  input  write,
  input  [7:0] data,
  input  [1:0] address,
  output [7:0] s
);

  wire [7:0] demultiplexer_1_out0, demultiplexer_1_out1, demultiplexer_1_out2, demultiplexer_1_out3,
       ram_1x8_1_s, ram_1x8_2_s, ram_1x8_3_s, ram_1x8_4_s;

  Demultiplexer #(.select(2), .width(8), .tristate("false")) demultiplexer_1 (
    .out0(demultiplexer_1_out0), .out1(demultiplexer_1_out1), .out2(demultiplexer_1_out2),
    .out3(demultiplexer_1_out3), .in(data), .sel(address));
  ram_1x8 ram_1x8_1 (.clock(clock), .write(write), .data(demultiplexer_1_out0), .s(ram_1x8_1_s));  // open: address
  ram_1x8 ram_1x8_2 (.clock(clock), .write(write), .data(demultiplexer_1_out1), .s(ram_1x8_2_s));  // open: address
  ram_1x8 ram_1x8_3 (.clock(clock), .write(write), .data(demultiplexer_1_out2), .s(ram_1x8_3_s));  // open: address
  ram_1x8 ram_1x8_4 (.clock(clock), .write(write), .data(demultiplexer_1_out3), .s(ram_1x8_4_s));  // open: address
  Multiplexer #(.select(2), .width(8)) multiplexer_1 (
    .in0(ram_1x8_1_s), .in1(ram_1x8_2_s), .in2(ram_1x8_3_s), .in3(ram_1x8_4_s), .out(s), .sel(address));

  // Notes on the sheet:
  //   RAM 1x8
  //   RAM 1x8
  //   RAM 1x8
  //   RAM 1x8
endmodule
