// Logisim project Guia14-405830.circ as structural Verilog: 4 circuits, main circuit Reg 4 bits
module Reg_4_bits (
  input  in_1,
  input  in_2,
  input  [3:0] in_3,
  input  in_4,
  output [3:0] out_5
);

  wire and_1_out;
  wire [3:0] d_ff_1_q;

  and and_1 (and_1_out, in_1, in_2);
  D_Flip_Flop #(.trigger("rising")) d_ff_1 (
    .clk(and_1_out), .D(in_3[0]), .Q(d_ff_1_q[0]), .reset(in_4));  // open: Qn, preset, en
  D_Flip_Flop #(.trigger("rising")) d_ff_2 (
    .clk(and_1_out), .D(in_3[1]), .Q(d_ff_1_q[1]), .reset(in_4));  // open: Qn, preset, en
  D_Flip_Flop #(.trigger("rising")) d_ff_3 (
    .clk(and_1_out), .D(in_3[2]), .Q(d_ff_1_q[2]), .reset(in_4));  // open: Qn, preset, en
  D_Flip_Flop #(.trigger("rising")) d_ff_4 (
    .clk(and_1_out), .D(in_3[3]), .Q(d_ff_1_q[3]), .reset(in_4));  // open: Qn, preset, en
  assign out_5 = {4{in_1}} & d_ff_1_q;  // AND_Gate and_2, 4 bits wide

  // Notes on the sheet:
  //   Pedro Siqueira - 405830
endmodule

module Exercicio01 (
  input  Mostrar,
  input  CLK,
  input  [3:0] \Endereço ,
  input  Ctrl_alt_del,
  output [3:0] out_5
);

  Reg_4_bits reg_4_bits_1 (.in_1(Mostrar), .in_2(CLK), .in_3(\Endereço ), .in_4(Ctrl_alt_del), .out_5(out_5));

  // Notes on the sheet:
  //   Pedro Siqueira - 405830
endmodule

module Exercicio02 (
  input  Mostrar,
  input  CLK,
  input  [7:0] in_3,
  input  ctrl_alt_del,
  output [7:0] out_5
);

  Reg_4_bits reg_4_bits_1 (.in_1(Mostrar), .in_2(CLK), .in_3(in_3[3:0]), .in_4(ctrl_alt_del), .out_5(out_5[3:0]));
  Reg_4_bits reg_4_bits_2 (.in_1(Mostrar), .in_2(CLK), .in_3(in_3[7:4]), .in_4(ctrl_alt_del), .out_5(out_5[7:4]));

  // Notes on the sheet:
  //   Pedro Siqueira - 405830
endmodule

module Exercicio03 (
  input  in_1,
  input  [7:0] in_2,
  input  in_3,
  input  [1:0] in_4,
  output [7:0] out_5
);

  wire demultiplexer_1_out0, demultiplexer_1_out1, demultiplexer_1_out2, demultiplexer_1_out3;
  wire [7:0] exercicio02_1_out_5, exercicio02_2_out_5, exercicio02_3_out_5, exercicio02_4_out_5;

  Demultiplexer #(.select(2), .width(1), .tristate("false")) demultiplexer_1 (
    .out0(demultiplexer_1_out0), .out1(demultiplexer_1_out1), .out2(demultiplexer_1_out2),
    .out3(demultiplexer_1_out3), .in(1'b1), .sel(in_4));
  Exercicio02 exercicio02_1 (
    .Mostrar(demultiplexer_1_out0), .CLK(in_1), .in_3(in_2), .ctrl_alt_del(in_3), .out_5(exercicio02_1_out_5));
  Exercicio02 exercicio02_2 (
    .Mostrar(demultiplexer_1_out1), .CLK(in_1), .in_3(in_2), .ctrl_alt_del(in_3), .out_5(exercicio02_2_out_5));
  Exercicio02 exercicio02_3 (
    .Mostrar(demultiplexer_1_out2), .CLK(in_1), .in_3(in_2), .ctrl_alt_del(in_3), .out_5(exercicio02_3_out_5));
  Exercicio02 exercicio02_4 (
    .Mostrar(demultiplexer_1_out3), .CLK(in_1), .in_3(in_2), .ctrl_alt_del(in_3), .out_5(exercicio02_4_out_5));
  assign out_5 = exercicio02_1_out_5 | exercicio02_2_out_5 | exercicio02_3_out_5 | exercicio02_4_out_5;  // OR_Gate or_1, 8 bits wide

  // Notes on the sheet:
  //   Pedro Siqueira - 405830
endmodule
