// Logisim project implementacao02.circ as structural Verilog: 2 circuits, main circuit main
module main (
  input  Endereco,
  input  [7:0] Input,
  input  Clear,
  output [7:0] Output
);

  wire clock_1_out;

  Clock #(.highDuration(1), .lowDuration(1)) clock_1 (.out(clock_1_out));
  registrador registrador_1 (
    .Endereco(Endereco), .Clock(clock_1_out), .Dado(Input[3:0]), .Clear(Clear), .out_5(Output[3:0]));
  registrador registrador_2 (
    .Endereco(Endereco), .Clock(clock_1_out), .Dado(Input[7:4]), .Clear(Clear), .out_5(Output[7:4]));

  // Notes on the sheet:
  //   Arquitetura de Computadores - Guia 14
  //   Implementar uma Memória RAM 1x8
  //   Tiago Menegaz de Melo Garcia             405844
endmodule

module registrador (
  input  Endereco,
  input  Clock,
  input  [3:0] Dado,
  input  Clear,
  output [3:0] out_5
);

  wire and_1_out;
  wire [3:0] d_ff_1_q;

  and and_1 (and_1_out, Endereco, Clock);
  D_Flip_Flop #(.trigger("rising")) d_ff_1 (
    .clk(and_1_out), .D(Dado[0]), .Q(d_ff_1_q[0]), .reset(Clear));  // open: Qn, preset, en
  D_Flip_Flop #(.trigger("rising")) d_ff_2 (
    .clk(and_1_out), .D(Dado[1]), .Q(d_ff_1_q[1]), .reset(Clear));  // open: Qn, preset, en
  D_Flip_Flop #(.trigger("rising")) d_ff_3 (
    .clk(and_1_out), .D(Dado[2]), .Q(d_ff_1_q[2]), .reset(Clear));  // open: Qn, preset, en
  D_Flip_Flop #(.trigger("rising")) d_ff_4 (
    .clk(and_1_out), .D(Dado[3]), .Q(d_ff_1_q[3]), .reset(Clear));  // open: Qn, preset, en
  assign out_5 = {4{Endereco}} & d_ff_1_q;  // AND_Gate and_2, 4 bits wide
endmodule
