// Logisim project implementacao03.circ as structural Verilog: 2 circuits, main circuit main
module main (
  input  Clear,
  input  [7:0] Input,
  input  [1:0] Endereco,
  output [7:0] Output
);

  wire clock_1_out;
  wire [7:0] registrador_1_out_5, registrador_2_out_5, registrador_3_out_5, registrador_4_out_5, undriven;

  Clock #(.highDuration(1), .lowDuration(1)) clock_1 (.out(clock_1_out));
  registrador registrador_1 (
    .Clock(clock_1_out), .Dado(undriven), .Clear(Clear), .out_5(registrador_1_out_5));  // open: Endereco
  registrador registrador_2 (
    .Clock(clock_1_out), .Dado(undriven), .Clear(Clear), .out_5(registrador_2_out_5));  // open: Endereco
  registrador registrador_3 (
    .Clock(clock_1_out), .Dado(Input), .Clear(Clear), .out_5(registrador_3_out_5));  // open: Endereco
  registrador registrador_4 (
    .Clock(clock_1_out), .Dado(Input), .Clear(Clear), .out_5(registrador_4_out_5));  // open: Endereco
  Multiplexer #(.select(2), .width(8)) multiplexer_1 (
    .in0(registrador_3_out_5), .in1(registrador_1_out_5), .in3(registrador_2_out_5), .out(Output),
    .sel(Endereco));  // open: in2

  // Notes on the sheet:
  //   Arquitetura de Computadores - Guia 14
  //   Implementar uma Memória RAM 4x8
  //   Tiago Menegaz de Melo Garcia             405844
endmodule

module registrador (
  input  Endereco,
  input  Clock,
  input  [7:0] Dado,
  input  Clear,
  output [7:0] out_5
);

  wire and_1_out;
  wire [7:0] d_ff_1_q;

  and and_1 (and_1_out, Endereco, Clock);
  D_Flip_Flop #(.trigger("rising")) d_ff_1 (
    .clk(and_1_out), .D(Dado[0]), .Q(d_ff_1_q[0]), .reset(Clear));  // open: Qn, preset, en
  D_Flip_Flop #(.trigger("rising")) d_ff_2 (
    .clk(and_1_out), .D(Dado[1]), .Q(d_ff_1_q[1]), .reset(Clear));  // open: Qn, preset, en
  D_Flip_Flop #(.trigger("rising")) d_ff_3 (
    .clk(and_1_out), .D(Dado[2]), .Q(d_ff_1_q[2]), .reset(Clear));  // open: Qn, preset, en
  D_Flip_Flop #(.trigger("rising")) d_ff_4 (
    .clk(and_1_out), .D(Dado[3]), .Q(d_ff_1_q[3]), .reset(Clear));  // open: Qn, preset, en
  D_Flip_Flop #(.trigger("rising")) d_ff_5 (
    .clk(and_1_out), .D(Dado[4]), .Q(d_ff_1_q[4]), .reset(Clear));  // open: Qn, preset, en
  D_Flip_Flop #(.trigger("rising")) d_ff_6 (
    .clk(and_1_out), .D(Dado[5]), .Q(d_ff_1_q[5]), .reset(Clear));  // open: Qn, preset, en
  D_Flip_Flop #(.trigger("rising")) d_ff_7 (
    .clk(and_1_out), .D(Dado[6]), .Q(d_ff_1_q[6]), .reset(Clear));  // open: Qn, preset, en
  D_Flip_Flop #(.trigger("rising")) d_ff_8 (
    .clk(and_1_out), .D(Dado[7]), .Q(d_ff_1_q[7]), .reset(Clear));  // open: Qn, preset, en
  assign out_5 = {8{Endereco}} & d_ff_1_q;  // AND_Gate and_2, 8 bits wide
endmodule
