// Logisim project guia 14.circ as structural Verilog
module _1x4 (
  input  clock,
  input  r___w,
  input  address,
  input  [3:0] dados,
  input  clear,
  output [3:0] saida
);

  wire and_1_out, not_1_out, not_2_out;
  wire [3:0] controlled_buffer_1_out, d_ff_1_q;

  not not_1 (not_1_out, clock);
  and and_1 (and_1_out, not_1_out, r___w);
  assign controlled_buffer_1_out = and_1_out ? dados : 4'bz;  // Controlled_Buffer controlled_buffer_1
  D_Flip_Flop #(.trigger("rising")) d_ff_1 (
    .clk(clock), .D(controlled_buffer_1_out[0]), .Q(d_ff_1_q[0]), .en(address), .reset(clear));  // open: Qn, preset
  D_Flip_Flop #(.trigger("rising")) d_ff_2 (
    .clk(clock), .D(controlled_buffer_1_out[1]), .Q(d_ff_1_q[1]), .en(address), .reset(clear));  // open: Qn, preset
  D_Flip_Flop #(.trigger("rising")) d_ff_3 (
    .clk(clock), .D(controlled_buffer_1_out[2]), .Q(d_ff_1_q[2]), .en(address), .reset(clear));  // open: Qn, preset
  D_Flip_Flop #(.trigger("rising")) d_ff_4 (
    .clk(clock), .D(controlled_buffer_1_out[3]), .Q(d_ff_1_q[3]), .en(address), .reset(clear));  // open: Qn, preset
  not not_2 (not_2_out, r___w);
  assign saida = not_2_out ? d_ff_1_q : 4'bz;  // Controlled_Buffer controlled_buffer_2

  // Notes on the sheet:
  //   Jéssica Daniela  - 407450
endmodule

module _1x8 (
  input  clock,
  input  r___w,
  input  address,
  input  [7:0] dados,
  input  clear,
  output [7:0] out_6
);

  _1x4 u_1x4_1 (.clock(clock), .r___w(r___w), .address(address), .dados(dados[3:0]), .clear(clear), .saida(out_6[3:0]));
  _1x4 u_1x4_2 (.clock(clock), .r___w(r___w), .address(address), .dados(dados[7:4]), .clear(clear), .saida(out_6[7:4]));
endmodule

module _4x8 (
  input  clock,
  input  r___w,
  input  [1:0] address,
  input  [7:0] dados,
  input  clear,
  output [7:0] saida
);

  wire demultiplexer_1_out0, demultiplexer_1_out1, demultiplexer_1_out2, demultiplexer_1_out3;
  wire [7:0] n1x8_1_out_6, n1x8_2_out_6, n1x8_3_out_6, n1x8_4_out_6;

  Demultiplexer #(.select(2), .width(1), .tristate("false")) demultiplexer_1 (
    .out0(demultiplexer_1_out0), .out1(demultiplexer_1_out1), .out2(demultiplexer_1_out2),
    .out3(demultiplexer_1_out3), .in(1'b1), .sel(address));
  _1x8 u_1x8_1 (
    .clock(clock), .r___w(r___w), .address(demultiplexer_1_out0), .dados(dados), .clear(clear),
    .out_6(n1x8_1_out_6));
  _1x8 u_1x8_2 (
    .clock(clock), .r___w(r___w), .address(demultiplexer_1_out1), .dados(dados), .clear(clear),
    .out_6(n1x8_2_out_6));
  _1x8 u_1x8_3 (
    .clock(clock), .r___w(r___w), .address(demultiplexer_1_out2), .dados(dados), .clear(clear),
    .out_6(n1x8_3_out_6));
  _1x8 u_1x8_4 (
    .clock(clock), .r___w(r___w), .address(demultiplexer_1_out3), .dados(dados), .clear(clear),
    .out_6(n1x8_4_out_6));
  Multiplexer #(.select(2), .width(8)) multiplexer_1 (
    .in0(n1x8_1_out_6), .in1(n1x8_2_out_6), .in2(n1x8_3_out_6), .in3(n1x8_4_out_6), .out(saida), .sel(address));
endmodule

module jk_1x4 (
  input  clock,
  input  r___w,
  input  address,
  input  [3:0] dados,
  input  clear,
  output [3:0] saida
);

  wire and_1_out, not_1_out, not_2_out, not_3_out, not_4_out, not_5_out, not_6_out;
  wire [3:0] controlled_buffer_1_out, j_k_ff_1_q;

  not not_1 (not_1_out, clock);
  and and_1 (and_1_out, not_1_out, r___w);
  assign controlled_buffer_1_out = and_1_out ? dados : 4'bz;  // Controlled_Buffer controlled_buffer_1
  not not_2 (not_2_out, controlled_buffer_1_out[0]);
  not not_3 (not_3_out, controlled_buffer_1_out[1]);
  not not_4 (not_4_out, controlled_buffer_1_out[2]);
  not not_5 (not_5_out, controlled_buffer_1_out[3]);
  not not_6 (not_6_out, r___w);
  J_K_Flip_Flop #(.trigger("rising")) j_k_ff_1 (
    .J(controlled_buffer_1_out[0]), .clk(clock), .K(not_2_out), .Q(j_k_ff_1_q[0]), .en(clock), .reset(clear));  // open: Qn, preset
  J_K_Flip_Flop #(.trigger("rising")) j_k_ff_2 (
    .J(controlled_buffer_1_out[1]), .clk(clock), .K(not_3_out), .Q(j_k_ff_1_q[1]), .en(address), .reset(clear));  // open: Qn, preset
  J_K_Flip_Flop #(.trigger("rising")) j_k_ff_3 (
    .J(controlled_buffer_1_out[2]), .clk(clock), .K(not_4_out), .Q(j_k_ff_1_q[2]), .en(address), .reset(clear));  // open: Qn, preset
  J_K_Flip_Flop #(.trigger("rising")) j_k_ff_4 (
    .J(controlled_buffer_1_out[3]), .clk(clock), .K(not_5_out), .Q(j_k_ff_1_q[3]), .en(address), .reset(clear));  // open: Qn, preset
  assign saida = not_6_out ? j_k_ff_1_q : 4'bz;  // Controlled_Buffer controlled_buffer_2
endmodule

module jk_2x4 (
  input  clock,
  input  r___w,
  input  address,
  input  [3:0] dados,
  input  clear,
  output [3:0] saida
);

  wire not_1_out, not_2_out;
  wire [3:0] jk_1x4_1_saida, jk_1x4_2_saida;

  jk_1x4 jk_1x4_1 (
    .clock(clock), .r___w(r___w), .address(not_1_out), .dados(dados), .clear(clear), .saida(jk_1x4_1_saida));
  not not_1 (not_1_out, address);
  jk_1x4 jk_1x4_2 (
    .clock(clock), .r___w(r___w), .address(address), .dados(dados), .clear(clear), .saida(jk_1x4_2_saida));
  assign saida = address ? jk_1x4_2_saida : 4'bz;  // Controlled_Buffer controlled_buffer_1
  not not_2 (not_2_out, address);
  assign saida = not_2_out ? jk_1x4_1_saida : 4'bz;  // Controlled_Buffer controlled_buffer_2
endmodule

module jk_2x8 (
  input  clock,
  input  r___w,
  input  address,
  input  [7:0] dados,
  input  clear,
  output [7:0] out_6
);

  jk_2x4 jk_2x4_1 (
    .clock(clock), .r___w(r___w), .address(address), .dados(dados[3:0]), .clear(clear), .saida(out_6[3:0]));
  jk_2x4 jk_2x4_2 (
    .clock(clock), .r___w(r___w), .address(address), .dados(dados[7:4]), .clear(clear), .saida(out_6[7:4]));
endmodule

module jk_4x8 (
  input  clock,
  input  r___w,
  input  address,
  input  [7:0] dados,
  input  clear,
  output [7:0] out_6
);

  wire not_1_out, not_2_out;
  wire [7:0] jk_2x8_1_out_6, jk_2x8_2_out_6;

  not not_1 (not_1_out, address);
  jk_2x8 jk_2x8_1 (
    .clock(clock), .r___w(r___w), .address(not_1_out), .dados(dados), .clear(clear), .out_6(jk_2x8_1_out_6));
  jk_2x8 jk_2x8_2 (
    .clock(clock), .r___w(r___w), .address(address), .dados(dados), .clear(clear), .out_6(jk_2x8_2_out_6));
  not not_2 (not_2_out, address);
  assign out_6 = address ? jk_2x8_2_out_6 : 8'bz;  // Controlled_Buffer controlled_buffer_1
  assign out_6 = not_2_out ? jk_2x8_1_out_6 : 8'bz;  // Controlled_Buffer controlled_buffer_2
endmodule
