// Logisim project Extras.circ as structural Verilog
module Registrador_4_bits (
  input  Clk,
  input  [3:0] Data_In,
  input  Clr,
  output [3:0] Data_Out
);

  wire not_1_out, not_2_out, not_3_out, not_4_out;

  not not_1 (not_1_out, Data_In[0]);
  not not_2 (not_2_out, Data_In[1]);
  not not_3 (not_3_out, Data_In[2]);
  not not_4 (not_4_out, Data_In[3]);
  J_K_Flip_Flop #(.trigger("rising")) j_k_ff_1 (
    .J(Data_In[0]), .clk(Clk), .K(not_1_out), .Q(Data_Out[0]), .reset(Clr));  // open: Qn, preset, en
  J_K_Flip_Flop #(.trigger("rising")) j_k_ff_2 (
    .J(Data_In[1]), .clk(Clk), .K(not_2_out), .Q(Data_Out[1]), .reset(Clr));  // open: Qn, preset, en
  J_K_Flip_Flop #(.trigger("rising")) j_k_ff_3 (
    .J(Data_In[2]), .clk(Clk), .K(not_3_out), .Q(Data_Out[2]), .reset(Clr));  // open: Qn, preset, en
  J_K_Flip_Flop #(.trigger("rising")) j_k_ff_4 (
    .J(Data_In[3]), .clk(Clk), .K(not_4_out), .Q(Data_Out[3]), .reset(Clr));  // open: Qn, preset, en
endmodule

module RAM_2X4 (
  input  Adr,
  input  Clk,
  input  [3:0] Data_In,
  input  Clr,
  output [3:0] Data_Out
);

  wire and_1_out, and_2_out;
  wire [3:0] and_3_out, and_4_out, registrador_4_bits_1_data_out, registrador_4_bits_2_data_out;
  wire [3:3] not_1_out;

  and and_1 (and_1_out, Adr, Clk);
  not not_1 (not_1_out[3], Adr);
  Registrador_4_bits registrador_4_bits_1 (
    .Clk(and_1_out), .Data_In(Data_In), .Clr(Clr), .Data_Out(registrador_4_bits_1_data_out));
  and and_2 (and_2_out, not_1_out[3], Clk);
  assign and_3_out = {4{Adr}} & registrador_4_bits_1_data_out;  // AND_Gate and_3, 4 bits wide
  assign and_4_out = {4{not_1_out[3]}} & registrador_4_bits_2_data_out;  // AND_Gate and_4, 4 bits wide
  Registrador_4_bits registrador_4_bits_2 (
    .Clk(and_2_out), .Data_In(Data_In), .Clr(Clr), .Data_Out(registrador_4_bits_2_data_out));
  assign Data_Out = and_3_out | and_4_out;  // OR_Gate or_1, 4 bits wide
endmodule

module RAM_4x8 (
  input  [1:0] Address,
  input  Clock,
  input  [7:0] Data_In,
  input  Clear,
  output [7:0] Data_Out
);

  RAM_2X4 ram_2x4_1 (.Adr(Address[0]), .Clk(Clock), .Data_In(Data_In[3:0]), .Clr(Clear), .Data_Out(Data_Out[3:0]));
  RAM_2X4 ram_2x4_2 (.Adr(Address[1]), .Clk(Clock), .Data_In(Data_In[7:4]), .Clr(Clear), .Data_Out(Data_Out[7:4]));
endmodule
