// Logisim project Guia14.circ as structural Verilog: 6 circuits, main circuit main
module main (
  input  [1:0] Address,
  input  [7:0] Data_In,
  input  Clear,
  output [7:0] Data_Out
);

  wire Clock_out;

  Clock #(.highDuration(1), .lowDuration(1)) Clock (.out(Clock_out));
  RAM_4x8 ram_4x8_1 (.Address(Address), .Clk(Clock_out), .Data_In(Data_In), .Clr(Clear), .Data_Out(Data_Out));
  Hex_Digit_Display hex_digit_display_1 (.value(Data_Out[7:4]));  // open: dp
  Hex_Digit_Display hex_digit_display_2 (.value(Data_Out[3:0]));  // open: dp

  // Notes on the sheet:
  //   Washington Luis de Souza Ramos
  //   407456
  //   Memória RAM de 1 byte e 4 endereços
endmodule

module Registrador_4_bits (
  input  Clk,
  input  [3:0] Data_In,
  input  Clr,
  output [3:0] Data_Out
);

  D_Flip_Flop #(.trigger("rising")) d_ff_1 (
    .clk(Clk), .D(Data_In[0]), .Q(Data_Out[0]), .reset(Clr));  // open: Qn, preset, en
  D_Flip_Flop #(.trigger("rising")) d_ff_2 (
    .clk(Clk), .D(Data_In[1]), .Q(Data_Out[1]), .reset(Clr));  // open: Qn, preset, en
  D_Flip_Flop #(.trigger("rising")) d_ff_3 (
    .clk(Clk), .D(Data_In[2]), .Q(Data_Out[2]), .reset(Clr));  // open: Qn, preset, en
  D_Flip_Flop #(.trigger("rising")) d_ff_4 (
    .clk(Clk), .D(Data_In[3]), .Q(Data_Out[3]), .reset(Clr));  // open: Qn, preset, en
endmodule

module \Memória  (
  input  Address,
  input  Read_Write,
  input  Clock,
  input  Clr,
  input  [3:0] Data,
  output [3:0] Out
);

  wire and_1_out;
  wire [3:0] registrador_4_bits_1_data_out;

  and and_1 (and_1_out, Address, Read_Write, Clock);
  Registrador_4_bits registrador_4_bits_1 (
    .Clk(and_1_out), .Data_In(Data), .Clr(Clr), .Data_Out(registrador_4_bits_1_data_out));
  assign Out = {4{Address}} & registrador_4_bits_1_data_out;  // AND_Gate and_2, 4 bits wide
endmodule

module RAM_1x4 (
  input  Address,
  input  Clock,
  input  Clr,
  input  [3:0] Data,
  output [3:0] Out
);

  wire and_1_out;
  wire [3:0] registrador_4_bits_1_data_out;

  and and_1 (and_1_out, Address, Clock);
  Registrador_4_bits registrador_4_bits_1 (
    .Clk(and_1_out), .Data_In(Data), .Clr(Clr), .Data_Out(registrador_4_bits_1_data_out));
  assign Out = {4{Address}} & registrador_4_bits_1_data_out;  // AND_Gate and_2, 4 bits wide
endmodule

module RAM_1x8 (
  input  Address,
  input  Clock,
  input  [7:0] Data,
  input  Clr,
  output [7:0] Out
);

  RAM_1x4 ram_1x4_1 (.Address(Address), .Clock(Clock), .Data(Data[3:0]), .Clr(Clr), .Out(Out[3:0]));
  RAM_1x4 ram_1x4_2 (.Address(Address), .Clock(Clock), .Data(Data[7:4]), .Clr(Clr), .Out(Out[7:4]));
endmodule

module RAM_4x8 (
  input  [1:0] Address,
  input  Clk,
  input  [7:0] Data_In,
  input  Clr,
  output [7:0] Data_Out
);

  wire and_1_out, and_2_out, and_3_out, and_4_out, not_1_out, not_2_out, not_3_out, not_4_out;
  wire [7:0] ram_1x8_1_out, ram_1x8_2_out, ram_1x8_3_out, ram_1x8_4_out;

  and and_1 (and_1_out, Address[0], not_1_out);
  not not_1 (not_1_out, Address[1]);
  not not_2 (not_2_out, Address[0]);
  and and_2 (and_2_out, not_2_out, not_3_out);
  not not_3 (not_3_out, Address[1]);
  and and_3 (and_3_out, Address[0], Address[1]);
  not not_4 (not_4_out, Address[0]);
  and and_4 (and_4_out, not_4_out, Address[1]);
  RAM_1x8 ram_1x8_1 (.Address(and_2_out), .Clock(Clk), .Data(Data_In), .Clr(Clr), .Out(ram_1x8_1_out));
  RAM_1x8 ram_1x8_2 (.Address(and_4_out), .Clock(Clk), .Data(Data_In), .Clr(Clr), .Out(ram_1x8_2_out));
  RAM_1x8 ram_1x8_3 (.Address(and_1_out), .Clock(Clk), .Data(Data_In), .Clr(Clr), .Out(ram_1x8_3_out));
  RAM_1x8 ram_1x8_4 (.Address(and_3_out), .Clock(Clk), .Data(Data_In), .Clr(Clr), .Out(ram_1x8_4_out));
  assign Data_Out = ram_1x8_3_out | ram_1x8_1_out | ram_1x8_4_out | ram_1x8_2_out;  // OR_Gate or_1, 8 bits wide

  // Notes on the sheet:
  //   Ctr Bus
  //   Data bus
  //   Adr bus
endmodule
