// Logisim project 412727.circ as structural Verilog: 9 circuits, main circuit main
module main (
);


  // Notes on the sheet:
  //   AUGUSTO FERREIRA ANDRADE DO CARMO - 412727 - GUIA 14
endmodule

module reg_4bits (
  input  clk,
  input  [3:0] Dados,
  input  [7:0] DataPath,
  output [3:0] out_4
);

  wire d_ff_1_q, d_ff_2_q, d_ff_3_q, d_ff_4_q;

  D_Flip_Flop #(.trigger("rising")) d_ff_1 (
    .clk(clk), .D(Dados[0]), .Q(d_ff_1_q), .en(DataPath[0]));  // open: Qn, preset, reset
  assign out_4[0] = DataPath[1] ? d_ff_1_q : 1'bz;  // Controlled_Buffer controlled_buffer_1
  D_Flip_Flop #(.trigger("rising")) d_ff_2 (
    .clk(clk), .D(Dados[1]), .Q(d_ff_2_q), .en(DataPath[2]));  // open: Qn, preset, reset
  assign out_4[1] = DataPath[3] ? d_ff_2_q : 1'bz;  // Controlled_Buffer controlled_buffer_2
  assign out_4[2] = DataPath[5] ? d_ff_3_q : 1'bz;  // Controlled_Buffer controlled_buffer_3
  D_Flip_Flop #(.trigger("rising")) d_ff_3 (
    .clk(clk), .D(Dados[2]), .Q(d_ff_3_q), .en(DataPath[4]));  // open: Qn, preset, reset
  D_Flip_Flop #(.trigger("rising")) d_ff_4 (
    .clk(clk), .D(Dados[3]), .Q(d_ff_4_q), .en(DataPath[6]));  // open: Qn, preset, reset
  assign out_4[3] = DataPath[7] ? d_ff_4_q : 1'bz;  // Controlled_Buffer controlled_buffer_4
endmodule

module Exercicio_1 (
  input  clk,
  input  w,
  input  addr,
  input  [3:0] dados,
  input  [7:0] datapath,
  output [3:0] out_6
);

  wire and_1_out, not_1_out;
  wire [3:0] reg_4bits_1_out_4;

  and and_1 (and_1_out, clk, w, addr);
  not not_1 (not_1_out, and_1_out);
  reg_4bits reg_4bits_1 (.clk(and_1_out), .Dados(dados), .DataPath(datapath), .out_4(reg_4bits_1_out_4));
  Multiplexer #(.select(1), .width(4)) multiplexer_1 (
    .in0(reg_4bits_1_out_4), .in1(reg_4bits_1_out_4), .out(out_6), .sel(not_1_out));
endmodule

module Exercicio_2 (
  input  clk,
  input  w,
  input  addr,
  input  [7:0] dados,
  input  [15:0] datapath,
  output [7:0] out_6
);

  wire not_1_out;
  wire [3:0] exercicio_1_1_out_6, exercicio_1_2_out_6;

  not not_1 (not_1_out, clk);
  Exercicio_1 exercicio_1_1 (
    .clk(clk), .w(w), .addr(addr), .dados(dados[3:0]), .datapath(datapath[7:0]), .out_6(exercicio_1_1_out_6));
  Exercicio_1 exercicio_1_2 (
    .clk(clk), .w(w), .addr(addr), .dados(dados[7:4]), .datapath(datapath[15:8]), .out_6(exercicio_1_2_out_6));
  Multiplexer #(.select(1), .width(8)) multiplexer_1 (
    .in0({exercicio_1_2_out_6, exercicio_1_1_out_6}), .in1({exercicio_1_2_out_6, exercicio_1_1_out_6}),
    .out(out_6), .sel(not_1_out));
endmodule

module Exercicio_3 (
  input  w,
  input  clk,
  input  [1:0] addres,
  input  [7:0] dados,
  input  [15:0] datapath,
  output [7:0] gravado
);

  wire demultiplexer_1_out0, demultiplexer_1_out1, demultiplexer_1_out2, demultiplexer_1_out3;
  wire [7:0] exercicio_2_1_out_6, exercicio_2_2_out_6, exercicio_2_3_out_6, exercicio_2_4_out_6;

  Demultiplexer #(.select(2), .width(1), .tristate("false")) demultiplexer_1 (
    .out0(demultiplexer_1_out0), .out1(demultiplexer_1_out1), .out2(demultiplexer_1_out2),
    .out3(demultiplexer_1_out3), .in(w), .sel(addres));
  Exercicio_2 exercicio_2_1 (
    .clk(clk), .w(w), .addr(demultiplexer_1_out3), .dados(dados), .datapath(datapath),
    .out_6(exercicio_2_1_out_6));
  Exercicio_2 exercicio_2_2 (
    .clk(clk), .w(w), .addr(demultiplexer_1_out2), .dados(dados), .datapath(datapath),
    .out_6(exercicio_2_2_out_6));
  Exercicio_2 exercicio_2_3 (
    .clk(clk), .w(w), .addr(demultiplexer_1_out1), .dados(dados), .datapath(datapath),
    .out_6(exercicio_2_3_out_6));
  Exercicio_2 exercicio_2_4 (
    .clk(clk), .w(w), .addr(demultiplexer_1_out0), .dados(dados), .datapath(datapath),
    .out_6(exercicio_2_4_out_6));
  Multiplexer #(.select(2), .width(8)) multiplexer_1 (
    .in0(exercicio_2_4_out_6), .in1(exercicio_2_3_out_6), .in2(exercicio_2_2_out_6),
    .in3(exercicio_2_1_out_6), .out(gravado), .sel(addres));
endmodule

module reg_4bits_jk (
  input  clk,
  input  [3:0] Dados,
  input  [7:0] DataPath,
  output [3:0] out_4
);

  wire j_k_ff_1_q, j_k_ff_2_q, j_k_ff_3_q, j_k_ff_4_q, not_1_out, not_2_out, not_3_out, not_4_out;

  not not_1 (not_1_out, Dados[0]);
  not not_2 (not_2_out, Dados[1]);
  not not_3 (not_3_out, Dados[2]);
  not not_4 (not_4_out, Dados[3]);
  assign out_4[0] = DataPath[1] ? j_k_ff_1_q : 1'bz;  // Controlled_Buffer controlled_buffer_1
  J_K_Flip_Flop #(.trigger("rising")) j_k_ff_1 (
    .J(Dados[0]), .clk(clk), .K(not_1_out), .Q(j_k_ff_1_q), .en(DataPath[0]));  // open: Qn, preset, reset
  assign out_4[1] = DataPath[3] ? j_k_ff_2_q : 1'bz;  // Controlled_Buffer controlled_buffer_2
  J_K_Flip_Flop #(.trigger("rising")) j_k_ff_2 (
    .J(Dados[1]), .clk(clk), .K(not_2_out), .Q(j_k_ff_2_q), .en(DataPath[2]));  // open: Qn, preset, reset
  assign out_4[2] = DataPath[5] ? j_k_ff_3_q : 1'bz;  // Controlled_Buffer controlled_buffer_3
  J_K_Flip_Flop #(.trigger("rising")) j_k_ff_3 (
    .J(Dados[2]), .clk(clk), .K(not_3_out), .Q(j_k_ff_3_q), .en(DataPath[4]));  // open: Qn, preset, reset
  assign out_4[3] = DataPath[7] ? j_k_ff_4_q : 1'bz;  // Controlled_Buffer controlled_buffer_4
  J_K_Flip_Flop #(.trigger("rising")) j_k_ff_4 (
    .J(Dados[3]), .clk(clk), .K(not_4_out), .Q(j_k_ff_4_q), .en(DataPath[6]));  // open: Qn, preset, reset
endmodule

module Exercicio_4_5 (
  input  w,
  input  clk,
  input  [1:0] addres,
  input  [7:0] dados,
  input  [15:0] datapath,
  output [7:0] gravado
);

  wire demultiplexer_1_out0, demultiplexer_1_out1, demultiplexer_1_out2, demultiplexer_1_out3;
  wire [7:0] exercicio_2_jk_1_out_6, exercicio_2_jk_2_out_6, exercicio_2_jk_3_out_6, exercicio_2_jk_4_out_6;

  Demultiplexer #(.select(2), .width(1), .tristate("false")) demultiplexer_1 (
    .out0(demultiplexer_1_out0), .out1(demultiplexer_1_out1), .out2(demultiplexer_1_out2),
    .out3(demultiplexer_1_out3), .in(w), .sel(addres));
  Exercicio_2_JK exercicio_2_jk_1 (
    .clk(clk), .w(w), .addr(demultiplexer_1_out3), .dados(dados), .datapath(datapath),
    .out_6(exercicio_2_jk_1_out_6));
  Exercicio_2_JK exercicio_2_jk_2 (
    .clk(clk), .w(w), .addr(demultiplexer_1_out2), .dados(dados), .datapath(datapath),
    .out_6(exercicio_2_jk_2_out_6));
  Exercicio_2_JK exercicio_2_jk_3 (
    .clk(clk), .w(w), .addr(demultiplexer_1_out1), .dados(dados), .datapath(datapath),
    .out_6(exercicio_2_jk_3_out_6));
  Exercicio_2_JK exercicio_2_jk_4 (
    .clk(clk), .w(w), .addr(demultiplexer_1_out0), .dados(dados), .datapath(datapath),
    .out_6(exercicio_2_jk_4_out_6));
  Multiplexer #(.select(2), .width(8)) multiplexer_1 (
    .in0(exercicio_2_jk_4_out_6), .in1(exercicio_2_jk_3_out_6), .in2(exercicio_2_jk_2_out_6),
    .in3(exercicio_2_jk_1_out_6), .out(gravado), .sel(addres));

  // Notes on the sheet:
  //   aqui já são os dois juntos, pois no de 4x8 já está 'contido' o 2x4
endmodule

module Exercicio_1_JK (
  input  clk,
  input  w,
  input  addr,
  input  [3:0] dados,
  input  [7:0] datapath,
  output [3:0] out_6
);

  wire and_1_out, not_1_out;
  wire [3:0] reg_4bits_jk_1_out_4;

  and and_1 (and_1_out, clk, w, addr);
  not not_1 (not_1_out, and_1_out);
  reg_4bits_jk reg_4bits_jk_1 (.clk(and_1_out), .Dados(dados), .DataPath(datapath), .out_4(reg_4bits_jk_1_out_4));
  Multiplexer #(.select(1), .width(4)) multiplexer_1 (
    .in0(reg_4bits_jk_1_out_4), .in1(reg_4bits_jk_1_out_4), .out(out_6), .sel(not_1_out));
endmodule

module Exercicio_2_JK (
  input  clk,
  input  w,
  input  addr,
  input  [7:0] dados,
  input  [15:0] datapath,
  output [7:0] out_6
);

  wire not_1_out;
  wire [3:0] exercicio_1_jk_1_out_6, exercicio_1_jk_2_out_6;

  not not_1 (not_1_out, clk);
  Exercicio_1_JK exercicio_1_jk_1 (
    .clk(clk), .w(w), .addr(addr), .dados(dados[3:0]), .datapath(datapath[7:0]),
    .out_6(exercicio_1_jk_1_out_6));
  Exercicio_1_JK exercicio_1_jk_2 (
    .clk(clk), .w(w), .addr(addr), .dados(dados[7:4]), .datapath(datapath[15:8]),
    .out_6(exercicio_1_jk_2_out_6));
  Multiplexer #(.select(1), .width(8)) multiplexer_1 (
    .in0({exercicio_1_jk_2_out_6, exercicio_1_jk_1_out_6}),
    .in1({exercicio_1_jk_2_out_6, exercicio_1_jk_1_out_6}), .out(out_6), .sel(not_1_out));
endmodule
