// Logisim project Memoria.circ as structural Verilog: 5 circuits, main circuit Registrador4bits
module Registrador4bits (
  input  Clock,
  input  [3:0] Variavel,
  input  [7:0] DataPath,
  output [3:0] S
);

  wire d_ff_1_q, d_ff_2_q, d_ff_3_q, d_ff_4_q;

  D_Flip_Flop #(.trigger("rising")) d_ff_1 (
    .clk(Clock), .D(Variavel[3]), .Q(d_ff_1_q), .en(DataPath[7]));  // open: Qn, preset, reset
  D_Flip_Flop #(.trigger("rising")) d_ff_2 (
    .clk(Clock), .D(Variavel[2]), .Q(d_ff_2_q), .en(DataPath[5]));  // open: Qn, preset, reset
  D_Flip_Flop #(.trigger("rising")) d_ff_3 (
    .clk(Clock), .D(Variavel[1]), .Q(d_ff_3_q), .en(DataPath[3]));  // open: Qn, preset, reset
  D_Flip_Flop #(.trigger("rising")) d_ff_4 (
    .clk(Clock), .D(Variavel[0]), .Q(d_ff_4_q), .en(DataPath[1]));  // open: Qn, preset, reset
  assign S[3] = DataPath[6] ? d_ff_1_q : 1'bz;  // Controlled_Buffer controlled_buffer_1
  assign S[2] = DataPath[4] ? d_ff_2_q : 1'bz;  // Controlled_Buffer controlled_buffer_2
  assign S[1] = DataPath[2] ? d_ff_3_q : 1'bz;  // Controlled_Buffer controlled_buffer_3
  assign S[0] = DataPath[0] ? d_ff_4_q : 1'bz;  // Controlled_Buffer controlled_buffer_4

  // Notes on the sheet:
  //   Fabricio Rodrigues de Souza - 412737
endmodule

module _1x4 (
  input  Clock,
  input  R_W,
  input  ADR,
  input  [3:0] Variavel,
  input  Enable,
  output [3:0] out_6
);

  wire and_1_out;

  and and_1 (and_1_out, Clock, R_W, ADR);
  FFD4Bits ffd4bits_1 (.Clock(and_1_out), .Data(Variavel), .Enable(Enable), .Output(out_6));

  // Notes on the sheet:
  //   Fabricio Rodrigues de Souza - 412737
endmodule

module _1x8 (
  input  Clock,
  input  R_W,
  input  Adr,
  input  [7:0] Variavel,
  input  Enable,
  output [7:0] out_6
);

  _1x4 u_1x4_1 (.Clock(Clock), .R_W(R_W), .ADR(Adr), .Variavel(Variavel[3:0]), .Enable(Enable), .out_6(out_6[3:0]));
  _1x4 u_1x4_2 (.Clock(Clock), .R_W(R_W), .ADR(Adr), .Variavel(Variavel[7:4]), .Enable(Enable), .out_6(out_6[7:4]));

  // Notes on the sheet:
  //   Fabricio Rodrigues de Souza - 412737
endmodule

module FFD4Bits (
  input  Clock,
  input  [3:0] Data,
  input  Enable,
  output [3:0] Output
);

  D_Flip_Flop #(.trigger("rising")) d_ff_1 (
    .clk(Clock), .D(Data[3]), .Q(Output[3]), .en(Enable));  // open: Qn, preset, reset
  D_Flip_Flop #(.trigger("rising")) d_ff_2 (
    .clk(Clock), .D(Data[2]), .Q(Output[2]), .en(Enable));  // open: Qn, preset, reset
  D_Flip_Flop #(.trigger("rising")) d_ff_3 (
    .clk(Clock), .D(Data[1]), .Q(Output[1]), .en(Enable));  // open: Qn, preset, reset
  D_Flip_Flop #(.trigger("rising")) d_ff_4 (
    .clk(Clock), .D(Data[0]), .Q(Output[0]), .en(Enable));  // open: Qn, preset, reset

  // Notes on the sheet:
  //   Fabricio Rodrigues de Souza - 412737
endmodule

module _4X8 (
  input  Clock,
  input  R_W,
  input  [7:0] Variavel,
  input  [1:0] Chave,
  input  Enable,
  output [7:0] Saida
);

  wire demultiplexer_1_out0, demultiplexer_1_out1, demultiplexer_1_out2, demultiplexer_1_out3;
  wire [7:0] n1x8_1_out_6, n1x8_2_out_6, n1x8_3_out_6, n1x8_4_out_6;

  Demultiplexer #(.select(2), .width(1), .tristate("false")) demultiplexer_1 (
    .out0(demultiplexer_1_out0), .out1(demultiplexer_1_out1), .out2(demultiplexer_1_out2),
    .out3(demultiplexer_1_out3), .in(1'b1), .sel(Chave));
  _1x8 u_1x8_1 (
    .Clock(R_W), .R_W(Clock), .Adr(demultiplexer_1_out0), .Variavel(Variavel), .Enable(Enable),
    .out_6(n1x8_1_out_6));
  _1x8 u_1x8_2 (
    .Clock(R_W), .R_W(Clock), .Adr(demultiplexer_1_out1), .Variavel(Variavel), .Enable(Enable),
    .out_6(n1x8_2_out_6));
  _1x8 u_1x8_3 (
    .Clock(R_W), .R_W(Clock), .Adr(demultiplexer_1_out2), .Variavel(Variavel), .Enable(Enable),
    .out_6(n1x8_3_out_6));
  _1x8 u_1x8_4 (
    .Clock(R_W), .R_W(Clock), .Adr(demultiplexer_1_out3), .Variavel(Variavel), .Enable(Enable),
    .out_6(n1x8_4_out_6));
  Multiplexer #(.select(2), .width(8)) multiplexer_1 (
    .in0(n1x8_1_out_6), .in1(n1x8_2_out_6), .in2(n1x8_3_out_6), .in3(n1x8_4_out_6), .out(Saida), .sel(Chave));

  // Notes on the sheet:
  //   Fabricio Rodrigues de Souza - 412737
endmodule
