// Logisim project Guia14.circ as structural Verilog
module Ex01___1x4 (
  input  [3:0] a,
  input  R_W,
  input  Clk,
  input  Adrss,
  input  Clr,
  output [3:0] out_6
);

  wire and_1_out, not_1_out, not_2_out;
  wire [3:0] controlled_buffer_1_out, d_ff_1_q;

  assign controlled_buffer_1_out = and_1_out ? a : 4'bz;  // Controlled_Buffer controlled_buffer_1
  and and_1 (and_1_out, R_W, not_1_out);
  not not_1 (not_1_out, Clk);
  D_Flip_Flop #(.trigger("rising")) d_ff_1 (
    .clk(Clk), .D(controlled_buffer_1_out[0]), .Q(d_ff_1_q[0]), .en(Adrss), .reset(Clr));  // open: Qn, preset
  D_Flip_Flop #(.trigger("rising")) d_ff_2 (
    .clk(Clk), .D(controlled_buffer_1_out[1]), .Q(d_ff_1_q[1]), .en(Adrss), .reset(Clr));  // open: Qn, preset
  D_Flip_Flop #(.trigger("rising")) d_ff_3 (
    .clk(Clk), .D(controlled_buffer_1_out[2]), .Q(d_ff_1_q[2]), .en(Adrss), .reset(Clr));  // open: Qn, preset
  D_Flip_Flop #(.trigger("rising")) d_ff_4 (
    .clk(Clk), .D(controlled_buffer_1_out[3]), .Q(d_ff_1_q[3]), .en(Adrss), .reset(Clr));  // open: Qn, preset
  assign out_6 = not_2_out ? d_ff_1_q : 4'bz;  // Controlled_Buffer controlled_buffer_2
  not not_2 (not_2_out, R_W);

  // Notes on the sheet:
  //   Lucas Teixeira - 415383
  //   Guardar na memoria quando R/W = 1, Adress = 1 e Clock sobe
endmodule

module Ex02___1x8 (
  input  R_W,
  input  Clock,
  input  Adress,
  input  Clear,
  input  [7:0] a,
  output [7:0] s
);

  Ex01___1x4 ex01_1x4_1 (.a(a[7:4]), .R_W(R_W), .Clk(Clock), .Adrss(Adress), .Clr(Clear), .out_6(s[7:4]));
  Ex01___1x4 ex01_1x4_2 (.a(a[3:0]), .R_W(R_W), .Clk(Clock), .Adrss(Adress), .Clr(Clear), .out_6(s[3:0]));

  // Notes on the sheet:
  //   Guardar na memoria quando R/W = 1, Adress = 1 e Clock sobe
  //   Lucas Teixeira - 415383
endmodule

module Ex03___4x8 (
  input  [7:0] a,
  input  R_W,
  input  Clock,
  input  Clear,
  input  [1:0] Adress,
  output [7:0] s
);

  wire demultiplexer_1_out0, demultiplexer_1_out1, demultiplexer_1_out2, demultiplexer_1_out3;
  wire [7:0] ex02_1x8_1_s, ex02_1x8_2_s, ex02_1x8_3_s, ex02_1x8_4_s;

  Demultiplexer #(.select(2), .width(1), .tristate("false")) demultiplexer_1 (
    .out0(demultiplexer_1_out0), .out1(demultiplexer_1_out1), .out2(demultiplexer_1_out2),
    .out3(demultiplexer_1_out3), .in(1'b1), .sel(Adress));
  Ex02___1x8 ex02_1x8_1 (
    .R_W(R_W), .Clock(Clock), .Adress(demultiplexer_1_out0), .Clear(Clear), .a(a), .s(ex02_1x8_1_s));
  Ex02___1x8 ex02_1x8_2 (
    .R_W(R_W), .Clock(Clock), .Adress(demultiplexer_1_out1), .Clear(Clear), .a(a), .s(ex02_1x8_2_s));
  Ex02___1x8 ex02_1x8_3 (
    .R_W(R_W), .Clock(Clock), .Adress(demultiplexer_1_out2), .Clear(Clear), .a(a), .s(ex02_1x8_3_s));
  Ex02___1x8 ex02_1x8_4 (
    .R_W(R_W), .Clock(Clock), .Adress(demultiplexer_1_out3), .Clear(Clear), .a(a), .s(ex02_1x8_4_s));
  Multiplexer #(.select(2), .width(8)) multiplexer_1 (
    .in0(ex02_1x8_1_s), .in1(ex02_1x8_2_s), .in2(ex02_1x8_3_s), .in3(ex02_1x8_4_s), .out(s), .sel(Adress));

  // Notes on the sheet:
  //   Guardar na memoria quando R/W = 1, Adress = 1 e Clock sobe
  //   Lucas Teixeira - 415383
endmodule

module Ex04___1x4 (
  input  [3:0] a,
  input  R_W,
  input  Clk,
  input  Adrss,
  input  Clr,
  output [3:0] out_6
);

  wire and_1_out, not_1_out, not_2_out, not_3_out, not_4_out, not_5_out, not_6_out;
  wire [3:0] controlled_buffer_1_out, j_k_ff_1_q;

  assign controlled_buffer_1_out = and_1_out ? a : 4'bz;  // Controlled_Buffer controlled_buffer_1
  and and_1 (and_1_out, R_W, not_1_out);
  not not_1 (not_1_out, Clk);
  not not_2 (not_2_out, controlled_buffer_1_out[0]);
  not not_3 (not_3_out, controlled_buffer_1_out[1]);
  not not_4 (not_4_out, controlled_buffer_1_out[2]);
  not not_5 (not_5_out, controlled_buffer_1_out[3]);
  J_K_Flip_Flop #(.trigger("rising")) j_k_ff_1 (
    .J(controlled_buffer_1_out[0]), .clk(Clk), .K(not_2_out), .Q(j_k_ff_1_q[0]), .en(Adrss), .reset(Clr));  // open: Qn, preset
  J_K_Flip_Flop #(.trigger("rising")) j_k_ff_2 (
    .J(controlled_buffer_1_out[1]), .clk(Clk), .K(not_3_out), .Q(j_k_ff_1_q[1]), .en(Adrss), .reset(Clr));  // open: Qn, preset
  J_K_Flip_Flop #(.trigger("rising")) j_k_ff_3 (
    .J(controlled_buffer_1_out[2]), .clk(Clk), .K(not_4_out), .Q(j_k_ff_1_q[2]), .en(Adrss), .reset(Clr));  // open: Qn, preset
  J_K_Flip_Flop #(.trigger("rising")) j_k_ff_4 (
    .J(controlled_buffer_1_out[3]), .clk(Clk), .K(not_5_out), .Q(j_k_ff_1_q[3]), .en(Adrss), .reset(Clr));  // open: Qn, preset
  assign out_6 = not_6_out ? j_k_ff_1_q : 4'bz;  // Controlled_Buffer controlled_buffer_2
  not not_6 (not_6_out, R_W);

  // Notes on the sheet:
  //   Lucas Teixeira - 415383
endmodule

module Ex04___2x4 (
  input  [3:0] a,
  input  R_W,
  input  Clock,
  input  Clear,
  input  Adress,
  output [3:0] s
);

  wire demultiplexer_1_out0, demultiplexer_1_out1;
  wire [3:0] ex04_1x4_1_out_6, ex04_1x4_2_out_6;

  Demultiplexer #(.select(1), .width(1), .tristate("false")) demultiplexer_1 (
    .out0(demultiplexer_1_out0), .out1(demultiplexer_1_out1), .in(1'b1), .sel(Adress));
  Ex04___1x4 ex04_1x4_1 (
    .a(a), .R_W(R_W), .Clk(Clock), .Adrss(demultiplexer_1_out0), .Clr(Clear), .out_6(ex04_1x4_1_out_6));
  Ex04___1x4 ex04_1x4_2 (
    .a(a), .R_W(R_W), .Clk(Clock), .Adrss(demultiplexer_1_out1), .Clr(Clear), .out_6(ex04_1x4_2_out_6));
  Multiplexer #(.select(1), .width(4)) multiplexer_1 (
    .in0(ex04_1x4_1_out_6), .in1(ex04_1x4_2_out_6), .out(s), .sel(Adress));

  // Notes on the sheet:
  //   Lucas Teixeira - 415383
endmodule

module Ex05___2x8 (
  input  R_W,
  input  Clock,
  input  Adress,
  input  Clear,
  input  [7:0] a,
  output [7:0] s
);

  Ex04___2x4 ex04_2x4_1 (.a(a[7:4]), .R_W(R_W), .Clock(Clock), .Clear(Clear), .Adress(Adress), .s(s[7:4]));
  Ex04___2x4 ex04_2x4_2 (.a(a[3:0]), .R_W(R_W), .Clock(Clock), .Clear(Clear), .Adress(Adress), .s(s[3:0]));

  // Notes on the sheet:
  //   Lucas Teixeira - 415383
endmodule

module Ex05___4x8 (
  input  R_W,
  input  Clock,
  input  Clear,
  input  [7:0] a,
  input  [1:0] Adress,
  output [7:0] s
);

  wire and_1_out, and_2_out, demultiplexer_1_out0, demultiplexer_1_out1, demultiplexer_1_out2,
       demultiplexer_1_out3, or_1_out, or_2_out;
  wire [7:0] controlled_buffer_1_out, controlled_buffer_2_out, ex05_2x8_1_s, ex05_2x8_2_s;

  Demultiplexer #(.select(2), .width(1), .tristate("false")) demultiplexer_1 (
    .out0(demultiplexer_1_out0), .out1(demultiplexer_1_out1), .out2(demultiplexer_1_out2),
    .out3(demultiplexer_1_out3), .in(1'b1), .sel(Adress));
  and and_1 (and_1_out, Adress[0], demultiplexer_1_out1);
  assign controlled_buffer_1_out = or_1_out ? a : 8'bz;  // Controlled_Buffer controlled_buffer_1
  and and_2 (and_2_out, Adress[1], demultiplexer_1_out3);
  or or_1 (or_1_out, demultiplexer_1_out0, demultiplexer_1_out1);
  Ex05___2x8 ex05_2x8_1 (
    .R_W(R_W), .Clock(Clock), .Adress(and_1_out), .Clear(Clear), .a(controlled_buffer_1_out), .s(ex05_2x8_1_s));
  Ex05___2x8 ex05_2x8_2 (
    .R_W(R_W), .Clock(Clock), .Adress(and_2_out), .Clear(Clear), .a(controlled_buffer_2_out), .s(ex05_2x8_2_s));
  assign controlled_buffer_2_out = or_2_out ? a : 8'bz;  // Controlled_Buffer controlled_buffer_2
  or or_2 (or_2_out, demultiplexer_1_out2, demultiplexer_1_out3);
  Multiplexer #(.select(2), .width(8)) multiplexer_1 (
    .in0(ex05_2x8_1_s), .in1(ex05_2x8_1_s), .in2(ex05_2x8_2_s), .in3(ex05_2x8_2_s), .out(s), .sel(Adress));

  // Notes on the sheet:
  //   Lucas Teixeira - 415383
  //   com o endereço selecionado
  //   Usei um Dmx para juntar a saída dele e juntei numa and
  //   Para não gravar erroneamente
  //   Como cada 2x8 usa um bit para direcionar pro registrador e seu endereço
  //   O Controled Buffer evita que o dado vai para as 2 "caixinhas"
endmodule
