// Logisim project Guia14.circ as structural Verilog
module RAM_1x4 (
  input  CLK,
  input  R___W,
  input  ADDRES,
  input  [3:0] IN,
  input  CLR,
  output [3:0] OUT
);

  wire and_1_out, and_2_out, not_1_out, not_2_out;
  wire [3:0] d_ff_1_q;

  and and_1 (and_1_out, CLK, R___W, ADDRES);
  not not_1 (not_1_out, R___W);
  not not_2 (not_2_out, CLK);
  D_Flip_Flop #(.trigger("rising")) d_ff_1 (
    .clk(and_1_out), .D(IN[0]), .Q(d_ff_1_q[0]), .reset(CLR));  // open: Qn, preset, en
  D_Flip_Flop #(.trigger("rising")) d_ff_2 (
    .clk(and_1_out), .D(IN[1]), .Q(d_ff_1_q[1]), .reset(CLR));  // open: Qn, preset, en
  D_Flip_Flop #(.trigger("rising")) d_ff_3 (
    .clk(and_1_out), .D(IN[2]), .Q(d_ff_1_q[2]), .reset(CLR));  // open: Qn, preset, en
  D_Flip_Flop #(.trigger("rising")) d_ff_4 (
    .clk(and_1_out), .D(IN[3]), .Q(d_ff_1_q[3]), .reset(CLR));  // open: Qn, preset, en
  assign OUT = and_2_out ? d_ff_1_q : 4'bz;  // Controlled_Buffer controlled_buffer_1
  and and_2 (and_2_out, not_1_out, not_2_out);

  // Notes on the sheet:
  //   Felipe Augusto
endmodule

module RAM_1x8 (
  input  CLK,
  input  R___W,
  input  ADDRES,
  input  [7:0] IN,
  input  CLR,
  output [7:0] OUT
);

  RAM_1x4 ram_1x4_1 (.CLK(CLK), .R___W(R___W), .ADDRES(ADDRES), .IN(IN[3:0]), .CLR(CLR), .OUT(OUT[3:0]));
  RAM_1x4 ram_1x4_2 (.CLK(CLK), .R___W(R___W), .ADDRES(ADDRES), .IN(IN[7:4]), .CLR(CLR), .OUT(OUT[7:4]));
endmodule

module RAM_4x8 (
  input  R_W,
  input  CLK,
  input  [1:0] ADDRRES,
  input  [7:0] IN,
  input  CLR,
  output [7:0] OUT
);

  wire demultiplexer_1_out0, demultiplexer_1_out1, demultiplexer_1_out2, demultiplexer_1_out3;
  wire [7:0] ram_1x8_1_out, ram_1x8_2_out, ram_1x8_3_out, ram_1x8_4_out;

  Demultiplexer #(.select(2), .width(1), .tristate("false")) demultiplexer_1 (
    .out0(demultiplexer_1_out0), .out1(demultiplexer_1_out1), .out2(demultiplexer_1_out2),
    .out3(demultiplexer_1_out3), .in(CLK), .sel(ADDRRES));
  RAM_1x8 ram_1x8_1 (.CLK(demultiplexer_1_out0), .R___W(CLK), .ADDRES(R_W), .IN(IN), .CLR(CLR), .OUT(ram_1x8_1_out));
  RAM_1x8 ram_1x8_2 (.CLK(demultiplexer_1_out1), .R___W(CLK), .ADDRES(R_W), .IN(IN), .CLR(CLR), .OUT(ram_1x8_2_out));
  RAM_1x8 ram_1x8_3 (.CLK(demultiplexer_1_out2), .R___W(CLK), .ADDRES(R_W), .IN(IN), .CLR(CLR), .OUT(ram_1x8_3_out));
  RAM_1x8 ram_1x8_4 (.CLK(demultiplexer_1_out3), .R___W(CLK), .ADDRES(R_W), .IN(IN), .CLR(CLR), .OUT(ram_1x8_4_out));
  Multiplexer #(.select(2), .width(8)) multiplexer_1 (
    .in0(ram_1x8_1_out), .in1(ram_1x8_2_out), .in2(ram_1x8_3_out), .in3(ram_1x8_4_out), .out(OUT),
    .sel(ADDRRES));
endmodule

module Registrador_4_bits (
  input  CLK,
  input  R___W,
  input  [3:0] IN,
  input  CLR,
  output [3:0] OUT
);

  wire and_1_out, and_2_out, not_1_out, not_2_out, not_3_out, not_4_out, not_5_out, not_6_out;
  wire [3:0] j_k_ff_1_q;

  and and_1 (and_1_out, CLK, R___W);
  not not_1 (not_1_out, R___W);
  not not_2 (not_2_out, CLK);
  J_K_Flip_Flop #(.trigger("rising")) j_k_ff_1 (
    .J(IN[0]), .clk(and_1_out), .K(not_3_out), .Q(j_k_ff_1_q[0]), .reset(CLR));  // open: Qn, preset, en
  not not_3 (not_3_out, IN[0]);
  J_K_Flip_Flop #(.trigger("rising")) j_k_ff_2 (
    .J(IN[1]), .clk(and_1_out), .K(not_4_out), .Q(j_k_ff_1_q[1]), .reset(CLR));  // open: Qn, preset, en
  not not_4 (not_4_out, IN[1]);
  J_K_Flip_Flop #(.trigger("rising")) j_k_ff_3 (
    .J(IN[2]), .clk(and_1_out), .K(not_5_out), .Q(j_k_ff_1_q[2]), .reset(CLR));  // open: Qn, preset, en
  not not_5 (not_5_out, IN[2]);
  J_K_Flip_Flop #(.trigger("rising")) j_k_ff_4 (
    .J(IN[3]), .clk(and_1_out), .K(not_6_out), .Q(j_k_ff_1_q[3]), .reset(CLR));  // open: Qn, preset, en
  not not_6 (not_6_out, IN[3]);
  assign OUT = and_2_out ? j_k_ff_1_q : 4'bz;  // Controlled_Buffer controlled_buffer_1
  and and_2 (and_2_out, not_1_out, not_2_out);

  // Notes on the sheet:
  //   Felipe Augusto Torres
endmodule

module RAM_2X4 (
  input  CLK,
  input  R___W,
  input  ADDRES,
  input  [3:0] OUT,
  input  [3:0] in_5,
  input  CLR
);

  wire demultiplexer_1_out0, demultiplexer_1_out1;
  wire [3:0] registrador_4_bits_1_out, registrador_4_bits_2_out;

  Demultiplexer #(.select(1), .width(1), .tristate("false")) demultiplexer_1 (
    .out0(demultiplexer_1_out0), .out1(demultiplexer_1_out1), .in(CLK), .sel(ADDRES));
  Registrador_4_bits registrador_4_bits_1 (
    .CLK(demultiplexer_1_out0), .R___W(R___W), .IN(in_5), .CLR(CLR), .OUT(registrador_4_bits_1_out));
  Registrador_4_bits registrador_4_bits_2 (
    .CLK(demultiplexer_1_out1), .R___W(R___W), .IN(in_5), .CLR(CLR), .OUT(registrador_4_bits_2_out));
  Multiplexer #(.select(1), .width(4)) multiplexer_1 (
    .in0(registrador_4_bits_1_out), .in1(registrador_4_bits_2_out), .out(OUT), .sel(ADDRES));

  // Notes on the sheet:
  //   Felipe Augusto Torres
  //   Obs: não encontrei o motivo do erro.
endmodule

module RAM_4X8 (
  input  CLK,
  input  [3:0] OUT,
  input  R___W,
  input  [1:0] ADDRES,
  input  [3:0] IN,
  input  CLR
);

  wire demultiplexer_1_out0, demultiplexer_1_out1, demultiplexer_2_out0, demultiplexer_2_out1;
  wire [3:0] multiplexer_1_out, undriven, undriven_2;

  Demultiplexer #(.select(1), .width(1), .tristate("false")) demultiplexer_1 (
    .out0(demultiplexer_1_out0), .out1(demultiplexer_1_out1), .in(ADDRES[0]), .sel(ADDRES[0]));
  Demultiplexer #(.select(1), .width(1), .tristate("false")) demultiplexer_2 (
    .out0(demultiplexer_2_out0), .out1(demultiplexer_2_out1), .in(ADDRES[0]), .sel(ADDRES[1]));
  RAM_2X4 ram_2x4_1 (
    .CLK(demultiplexer_1_out0), .R___W(R___W), .ADDRES(demultiplexer_2_out0), .in_5(IN), .CLR(CLR),
    .OUT(undriven));
  RAM_2X4 ram_2x4_2 (
    .CLK(demultiplexer_1_out1), .R___W(R___W), .ADDRES(demultiplexer_2_out1), .in_5(IN), .CLR(CLR),
    .OUT(undriven_2));
  Multiplexer #(.select(1), .width(4)) multiplexer_1 (
    .in0(undriven), .in1(undriven_2), .out(multiplexer_1_out));  // open: sel

  assign CLK = ADDRES[0];
endmodule
