// Logisim project Logisim_Guia14.circ as structural Verilog
module Ram_1X4 (
  input  clock,
  input  [3:0] Dados,
  input  \Endereço ,
  input  clear,
  input  R_W,
  output [3:0] Output
);

  wire and_1_out, not_1_out, not_2_out;
  wire [3:0] controlled_buffer_1_out, d_ff_1_q;

  not not_1 (not_1_out, clock);
  not not_2 (not_2_out, R_W);
  assign controlled_buffer_1_out = and_1_out ? Dados : 4'bz;  // Controlled_Buffer controlled_buffer_1
  and and_1 (and_1_out, not_1_out, R_W);
  D_Flip_Flop #(.trigger("rising")) d_ff_1 (
    .clk(clock), .D(controlled_buffer_1_out[0]), .Q(d_ff_1_q[0]), .en(\Endereço ), .reset(clear));  // open: Qn, preset
  D_Flip_Flop #(.trigger("rising")) d_ff_2 (
    .clk(clock), .D(controlled_buffer_1_out[1]), .Q(d_ff_1_q[1]), .en(\Endereço ), .reset(clear));  // open: Qn, preset
  D_Flip_Flop #(.trigger("rising")) d_ff_3 (
    .clk(clock), .D(controlled_buffer_1_out[2]), .Q(d_ff_1_q[2]), .en(\Endereço ), .reset(clear));  // open: Qn, preset
  D_Flip_Flop #(.trigger("rising")) d_ff_4 (
    .clk(clock), .D(controlled_buffer_1_out[3]), .Q(d_ff_1_q[3]), .en(\Endereço ), .reset(clear));  // open: Qn, preset
  assign Output = not_2_out ? d_ff_1_q : 4'bz;  // Controlled_Buffer controlled_buffer_2

  // Notes on the sheet:
  //   Jonathan Felipe Xavier  Matricula 415704
endmodule

module Ram_1X8 (
  input  clock,
  input  [7:0] Dados,
  input  \Endereço ,
  input  R_W,
  input  clear,
  output [7:0] Output
);

  Ram_1X4 ram_1x4_1 (
    .clock(clock), .Dados(Dados[7:4]), .\Endereço (\Endereço ), .clear(clear), .R_W(R_W), .Output(Output[7:4]));
  Ram_1X4 ram_1x4_2 (
    .clock(clock), .Dados(Dados[3:0]), .\Endereço (\Endereço ), .clear(clear), .R_W(R_W), .Output(Output[3:0]));

  // Notes on the sheet:
  //   Jonathan Felipe Xavier  Matricula 415704
endmodule

module Ram_4X8 (
  input  clock,
  input  [7:0] Dados,
  input  [1:0] \Endereço ,
  input  R_W,
  input  clear,
  output [7:0] Output
);

  wire demultiplexer_1_out0, demultiplexer_1_out1, demultiplexer_1_out2, demultiplexer_1_out3;
  wire [7:0] ram_1x8_1_output, ram_1x8_2_output, ram_1x8_3_output, ram_1x8_4_output;

  Demultiplexer #(.select(2), .width(1), .tristate("false")) demultiplexer_1 (
    .out0(demultiplexer_1_out0), .out1(demultiplexer_1_out1), .out2(demultiplexer_1_out2),
    .out3(demultiplexer_1_out3), .in(1'b1), .sel(\Endereço ));
  Ram_1X8 ram_1x8_1 (
    .clock(clock), .Dados(Dados), .\Endereço (demultiplexer_1_out0), .R_W(R_W), .clear(clear),
    .Output(ram_1x8_1_output));
  Ram_1X8 ram_1x8_2 (
    .clock(clock), .Dados(Dados), .\Endereço (demultiplexer_1_out1), .R_W(R_W), .clear(clear),
    .Output(ram_1x8_2_output));
  Multiplexer #(.select(2), .width(8)) multiplexer_1 (
    .in0(ram_1x8_1_output), .in1(ram_1x8_2_output), .in2(ram_1x8_3_output), .in3(ram_1x8_4_output),
    .out(Output), .sel(\Endereço ));
  Ram_1X8 ram_1x8_3 (
    .clock(clock), .Dados(Dados), .\Endereço (demultiplexer_1_out2), .R_W(R_W), .clear(clear),
    .Output(ram_1x8_3_output));
  Ram_1X8 ram_1x8_4 (
    .clock(clock), .Dados(Dados), .\Endereço (demultiplexer_1_out3), .R_W(R_W), .clear(clear),
    .Output(ram_1x8_4_output));

  // Notes on the sheet:
  //   Jonathan Felipe Xavier  Matricula 415704
endmodule

module RamJK_1X4 (
  input  clock,
  input  [3:0] Dados,
  input  \Endereço ,
  input  clear,
  input  R_W,
  output [3:0] Output
);

  wire and_1_out, not_1_out, not_2_out, not_3_out, not_4_out, not_5_out, not_6_out;
  wire [3:0] controlled_buffer_1_out, j_k_ff_1_q;

  not not_1 (not_1_out, clock);
  not not_2 (not_2_out, R_W);
  assign controlled_buffer_1_out = and_1_out ? Dados : 4'bz;  // Controlled_Buffer controlled_buffer_1
  and and_1 (and_1_out, not_1_out, R_W);
  J_K_Flip_Flop #(.trigger("rising")) j_k_ff_1 (
    .J(controlled_buffer_1_out[0]), .clk(clock), .K(not_3_out), .Q(j_k_ff_1_q[0]), .en(\Endereço ),
    .reset(clear));  // open: Qn, preset
  not not_3 (not_3_out, controlled_buffer_1_out[0]);
  J_K_Flip_Flop #(.trigger("rising")) j_k_ff_2 (
    .J(controlled_buffer_1_out[1]), .clk(clock), .K(not_4_out), .Q(j_k_ff_1_q[1]), .en(\Endereço ),
    .reset(clear));  // open: Qn, preset
  not not_4 (not_4_out, controlled_buffer_1_out[1]);
  J_K_Flip_Flop #(.trigger("rising")) j_k_ff_3 (
    .J(controlled_buffer_1_out[2]), .clk(clock), .K(not_5_out), .Q(j_k_ff_1_q[2]), .en(\Endereço ),
    .reset(clear));  // open: Qn, preset
  not not_5 (not_5_out, controlled_buffer_1_out[2]);
  J_K_Flip_Flop #(.trigger("rising")) j_k_ff_4 (
    .J(controlled_buffer_1_out[3]), .clk(clock), .K(not_6_out), .Q(j_k_ff_1_q[3]), .en(\Endereço ),
    .reset(clear));  // open: Qn, preset
  not not_6 (not_6_out, controlled_buffer_1_out[3]);
  assign Output = not_2_out ? j_k_ff_1_q : 4'bz;  // Controlled_Buffer controlled_buffer_2

  // Notes on the sheet:
  //   Jonathan Felipe Xavier  Matricula 415704
endmodule

module RamJK_2X4 (
  input  clock,
  input  [3:0] Dados,
  input  \Endereço ,
  input  clear,
  input  R_W,
  output [3:0] Output
);

  wire not_1_out, not_2_out;
  wire [3:0] ramjk_1x4_1_output, ramjk_1x4_2_output;

  not not_1 (not_1_out, \Endereço );
  RamJK_1X4 ramjk_1x4_1 (
    .clock(clock), .Dados(Dados), .\Endereço (not_1_out), .clear(clear), .R_W(R_W),
    .Output(ramjk_1x4_1_output));
  not not_2 (not_2_out, \Endereço );
  assign Output = not_2_out ? ramjk_1x4_1_output : 4'bz;  // Controlled_Buffer controlled_buffer_1
  RamJK_1X4 ramjk_1x4_2 (
    .clock(clock), .Dados(Dados), .\Endereço (\Endereço ), .clear(clear), .R_W(R_W),
    .Output(ramjk_1x4_2_output));
  assign Output = \Endereço  ? ramjk_1x4_2_output : 4'bz;  // Controlled_Buffer controlled_buffer_2

  // Notes on the sheet:
  //   Jonathan Felipe Xavier  Matricula 415704
endmodule

module RamJK_2X8 (
  input  clock,
  input  [7:0] Dados,
  input  \Endereço ,
  input  R_W,
  input  clear,
  output [7:0] Output
);

  RamJK_2X4 ramjk_2x4_1 (
    .clock(clock), .Dados(Dados[7:4]), .\Endereço (\Endereço ), .clear(clear), .R_W(R_W), .Output(Output[7:4]));
  RamJK_2X4 ramjk_2x4_2 (
    .clock(clock), .Dados(Dados[3:0]), .\Endereço (\Endereço ), .clear(clear), .R_W(R_W), .Output(Output[3:0]));

  // Notes on the sheet:
  //   Jonathan Felipe Xavier  Matricula 415704
endmodule

module RamJK_4X8 (
  input  clock,
  input  [7:0] Dados,
  input  [1:0] \Endereço ,
  input  R_W,
  input  clear,
  output [7:0] Output
);

  wire controlled_buffer_1_out, not_1_out, not_2_out;
  wire [7:0] ramjk_2x8_1_output, ramjk_2x8_2_output;

  not not_1 (not_1_out, \Endereço [1]);
  assign controlled_buffer_1_out = not_1_out ? \Endereço [0] : 1'bz;  // Controlled_Buffer controlled_buffer_1
  RamJK_2X8 ramjk_2x8_1 (
    .clock(clock), .Dados(Dados), .\Endereço (controlled_buffer_1_out), .R_W(R_W), .clear(clear),
    .Output(ramjk_2x8_1_output));
  not not_2 (not_2_out, \Endereço [1]);
  assign Output = not_2_out ? ramjk_2x8_1_output : 8'bz;  // Controlled_Buffer controlled_buffer_2
  assign controlled_buffer_1_out = \Endereço [1] ? \Endereço [0] : 1'bz;  // Controlled_Buffer controlled_buffer_3
  RamJK_2X8 ramjk_2x8_2 (
    .clock(clock), .Dados(Dados), .\Endereço (controlled_buffer_1_out), .R_W(R_W), .clear(clear),
    .Output(ramjk_2x8_2_output));
  assign Output = \Endereço [1] ? ramjk_2x8_2_output : 8'bz;  // Controlled_Buffer controlled_buffer_4

  // Notes on the sheet:
  //   Jonathan Felipe Xavier  Matricula 415704
endmodule
