// Logisim project Exercicios_Guia14.circ as structural Verilog: 9 circuits, main circuit memória 2x1
module memoria_1X1 (
  input  endereco,
  input  r_w,
  input  clk,
  input  dado,
  input  clr,
  output out_6
);

  wire and_1_out, d_ff_1_q, not_1_out;

  and and_1 (and_1_out, endereco, r_w, clk);
  D_Flip_Flop #(.trigger("rising")) d_ff_1 (
    .clk(and_1_out), .D(dado), .Q(d_ff_1_q), .reset(clr));  // open: Qn, preset, en
  assign out_6 = not_1_out ? d_ff_1_q : 1'bz;  // Controlled_Buffer controlled_buffer_1
  not not_1 (not_1_out, clk);
endmodule

module \memória_2x1  (
  input  in_1,
  input  in_2,
  input  in_3,
  input  in_4,
  output out_5,
  output out_6
);

  wire clock_1_out, not_1_out;

  Clock #(.highDuration(1), .lowDuration(1)) clock_1 (.out(clock_1_out));
  not not_1 (not_1_out, in_1);
  memoria_1X1 memoria_1x1_1 (
    .endereco(not_1_out), .r_w(in_2), .clk(clock_1_out), .dado(in_3), .clr(in_4), .out_6(out_5));
  memoria_1X1 memoria_1x1_2 (.endereco(in_1), .r_w(in_2), .clk(clock_1_out), .dado(in_3), .clr(in_4), .out_6(out_6));
endmodule

module \memória_1X4  (
  input  ADDR,
  input  R_W,
  input  CLK,
  input  [3:0] DADOS,
  input  CLR,
  output [3:0] SAIDA
);

  wire and_1_out, not_1_out;
  wire [3:0] d_ff_1_q;

  and and_1 (and_1_out, ADDR, R_W, CLK);
  D_Flip_Flop #(.trigger("rising")) d_ff_1 (
    .clk(and_1_out), .D(DADOS[0]), .Q(d_ff_1_q[0]), .reset(CLR));  // open: Qn, preset, en
  D_Flip_Flop #(.trigger("rising")) d_ff_2 (
    .clk(and_1_out), .D(DADOS[1]), .Q(d_ff_1_q[1]), .reset(CLR));  // open: Qn, preset, en
  D_Flip_Flop #(.trigger("rising")) d_ff_3 (
    .clk(and_1_out), .D(DADOS[2]), .Q(d_ff_1_q[2]), .reset(CLR));  // open: Qn, preset, en
  not not_1 (not_1_out, CLK);
  D_Flip_Flop #(.trigger("rising")) d_ff_4 (
    .clk(and_1_out), .D(DADOS[3]), .Q(d_ff_1_q[3]), .reset(CLR));  // open: Qn, preset, en
  assign SAIDA = not_1_out ? d_ff_1_q : 4'bz;  // Controlled_Buffer controlled_buffer_1

  // Notes on the sheet:
  //   Memória 1x4
  //   flip-flop D
  //   Marcos Felipe Martins Silva-415719
endmodule

module \memória_1x8  (
  input  ADDR,
  input  R_W,
  input  CLK,
  input  [7:0] DADOS,
  input  CLR,
  output [7:0] SAIDA
);

  \memória_1X4  \memória_1x4_1  (.ADDR(ADDR), .R_W(R_W), .CLK(CLK), .DADOS(DADOS[3:0]), .CLR(CLR), .SAIDA(SAIDA[3:0]));
  \memória_1X4  \memória_1x4_2  (.ADDR(ADDR), .R_W(R_W), .CLK(CLK), .DADOS(DADOS[7:4]), .CLR(CLR), .SAIDA(SAIDA[7:4]));

  // Notes on the sheet:
  //   Memória 1x8
  //   flip-flop D
  //   Marcos Felipe Martins Silva-415719
endmodule

module \memória_4x8  (
  input  R_W,
  input  CLK,
  input  [7:0] DADOS,
  input  [1:0] ADDR,
  input  CLR,
  output [7:0] SAIDA
);

  wire demultiplexer_1_out0, demultiplexer_1_out1, demultiplexer_1_out2, demultiplexer_1_out3;
  wire [7:0] \memória_1x8_1_saida , \memória_1x8_2_saida , \memória_1x8_3_saida , \memória_1x8_4_saida ;

  Demultiplexer #(.select(2), .width(1), .tristate("false")) demultiplexer_1 (
    .out0(demultiplexer_1_out0), .out1(demultiplexer_1_out1), .out2(demultiplexer_1_out2),
    .out3(demultiplexer_1_out3), .in(1'b1), .sel(ADDR));
  \memória_1x8  \memória_1x8_1  (
    .ADDR(demultiplexer_1_out0), .R_W(R_W), .CLK(CLK), .DADOS(DADOS), .CLR(CLR), .SAIDA(\memória_1x8_1_saida ));
  \memória_1x8  \memória_1x8_2  (
    .ADDR(demultiplexer_1_out1), .R_W(R_W), .CLK(CLK), .DADOS(DADOS), .CLR(CLR), .SAIDA(\memória_1x8_2_saida ));
  \memória_1x8  \memória_1x8_3  (
    .ADDR(demultiplexer_1_out2), .R_W(R_W), .CLK(CLK), .DADOS(DADOS), .CLR(CLR), .SAIDA(\memória_1x8_3_saida ));
  \memória_1x8  \memória_1x8_4  (
    .ADDR(demultiplexer_1_out3), .R_W(R_W), .CLK(CLK), .DADOS(DADOS), .CLR(CLR), .SAIDA(\memória_1x8_4_saida ));
  Multiplexer #(.select(2), .width(8)) multiplexer_1 (
    .in0(\memória_1x8_1_saida ), .in1(\memória_1x8_2_saida ), .in2(\memória_1x8_3_saida ),
    .in3(\memória_1x8_4_saida ), .out(SAIDA), .sel(ADDR));

  // Notes on the sheet:
  //   Memória 4x8
  //   flip-flop D
  //   Marcos Felipe Martins Silva-415719
endmodule

module \memória_1x4__flip_flop_JK  (
  input  ADDR,
  input  R_W,
  input  CLK,
  input  [3:0] DADOS,
  input  CLR,
  output [3:0] SAIDA
);

  wire and_1_out, not_1_out, not_2_out, not_3_out, not_4_out, not_5_out;
  wire [3:0] j_k_ff_1_q;

  and and_1 (and_1_out, ADDR, R_W, CLK);
  not not_1 (not_1_out, DADOS[0]);
  J_K_Flip_Flop #(.trigger("rising")) j_k_ff_1 (
    .J(DADOS[0]), .clk(and_1_out), .K(not_1_out), .Q(j_k_ff_1_q[0]), .reset(CLR));  // open: Qn, preset, en
  J_K_Flip_Flop #(.trigger("rising")) j_k_ff_2 (
    .J(DADOS[1]), .clk(and_1_out), .K(not_2_out), .Q(j_k_ff_1_q[1]), .reset(CLR));  // open: Qn, preset, en
  not not_2 (not_2_out, DADOS[1]);
  J_K_Flip_Flop #(.trigger("rising")) j_k_ff_3 (
    .J(DADOS[2]), .clk(and_1_out), .K(not_3_out), .Q(j_k_ff_1_q[2]), .reset(CLR));  // open: Qn, preset, en
  not not_3 (not_3_out, DADOS[2]);
  J_K_Flip_Flop #(.trigger("rising")) j_k_ff_4 (
    .J(DADOS[3]), .clk(and_1_out), .K(not_4_out), .Q(j_k_ff_1_q[3]), .reset(CLR));  // open: Qn, preset, en
  not not_4 (not_4_out, DADOS[3]);
  assign SAIDA = not_5_out ? j_k_ff_1_q : 4'bz;  // Controlled_Buffer controlled_buffer_1
  not not_5 (not_5_out, CLK);

  // Notes on the sheet:
  //   Memória 1x4
  //   flip-flop JK
  //   Marcos Felipe Martins Silva-415719
endmodule

module \memória_2x4__flip_flop_JK  (
  input  R_W,
  input  CLK,
  input  [3:0] DADOS,
  input  ADDR,
  input  CLR,
  output [3:0] SAIDA
);

  wire demultiplexer_1_out0, demultiplexer_1_out1;
  wire [3:0] \memória_1x4_flip_flop_jk_1_saida , \memória_1x4_flip_flop_jk_2_saida ;

  Demultiplexer #(.select(1), .width(1), .tristate("false")) demultiplexer_1 (
    .out0(demultiplexer_1_out0), .out1(demultiplexer_1_out1), .in(1'b1), .sel(ADDR));
  \memória_1x4__flip_flop_JK  \memória_1x4_flip_flop_jk_1  (
    .ADDR(demultiplexer_1_out0), .R_W(R_W), .CLK(CLK), .DADOS(DADOS), .CLR(CLR),
    .SAIDA(\memória_1x4_flip_flop_jk_1_saida ));
  \memória_1x4__flip_flop_JK  \memória_1x4_flip_flop_jk_2  (
    .ADDR(demultiplexer_1_out1), .R_W(R_W), .CLK(CLK), .DADOS(DADOS), .CLR(CLR),
    .SAIDA(\memória_1x4_flip_flop_jk_2_saida ));
  Multiplexer #(.select(1), .width(4)) multiplexer_1 (
    .in0(\memória_1x4_flip_flop_jk_1_saida ), .in1(\memória_1x4_flip_flop_jk_2_saida ), .out(SAIDA),
    .sel(ADDR));

  // Notes on the sheet:
  //   Memória 2x4 
  //   flip-flop JK
  //   Marcos Felipe Martins Silva-415719
endmodule

module \memória_1x8__flip_flop_JK  (
  input  ADDR,
  input  R_W,
  input  CLK,
  input  [7:0] DADOS,
  input  CLR,
  output [7:0] SAIDA
);

  \memória_1x4__flip_flop_JK  \memória_1x4_flip_flop_jk_1  (
    .ADDR(ADDR), .R_W(R_W), .CLK(CLK), .DADOS(DADOS[3:0]), .CLR(CLR), .SAIDA(SAIDA[3:0]));
  \memória_1x4__flip_flop_JK  \memória_1x4_flip_flop_jk_2  (
    .ADDR(ADDR), .R_W(R_W), .CLK(CLK), .DADOS(DADOS[7:4]), .CLR(CLR), .SAIDA(SAIDA[7:4]));

  // Notes on the sheet:
  //   Memória 1x8
  //   flip-flop JK
  //   Marcos Felipe Martins Silva-415719
endmodule

module \memória_4x8__flip_flop_JK  (
  input  R_W,
  input  CLK,
  input  [7:0] DADOS,
  input  [1:0] ADDR,
  input  CLR,
  output [7:0] SAIDA
);

  wire demultiplexer_1_out0, demultiplexer_1_out1, demultiplexer_1_out2, demultiplexer_1_out3;
  wire [7:0] \memória_1x8_flip_flop_jk_1_saida , \memória_1x8_flip_flop_jk_2_saida ,
       \memória_1x8_flip_flop_jk_3_saida , \memória_1x8_flip_flop_jk_4_saida ;

  Demultiplexer #(.select(2), .width(1), .tristate("false")) demultiplexer_1 (
    .out0(demultiplexer_1_out0), .out1(demultiplexer_1_out1), .out2(demultiplexer_1_out2),
    .out3(demultiplexer_1_out3), .in(1'b1), .sel(ADDR));
  \memória_1x8__flip_flop_JK  \memória_1x8_flip_flop_jk_1  (
    .ADDR(demultiplexer_1_out0), .R_W(R_W), .CLK(CLK), .DADOS(DADOS), .CLR(CLR),
    .SAIDA(\memória_1x8_flip_flop_jk_1_saida ));
  \memória_1x8__flip_flop_JK  \memória_1x8_flip_flop_jk_2  (
    .ADDR(demultiplexer_1_out1), .R_W(R_W), .CLK(CLK), .DADOS(DADOS), .CLR(CLR),
    .SAIDA(\memória_1x8_flip_flop_jk_2_saida ));
  \memória_1x8__flip_flop_JK  \memória_1x8_flip_flop_jk_3  (
    .ADDR(demultiplexer_1_out2), .R_W(R_W), .CLK(CLK), .DADOS(DADOS), .CLR(CLR),
    .SAIDA(\memória_1x8_flip_flop_jk_3_saida ));
  \memória_1x8__flip_flop_JK  \memória_1x8_flip_flop_jk_4  (
    .ADDR(demultiplexer_1_out3), .R_W(R_W), .CLK(CLK), .DADOS(DADOS), .CLR(CLR),
    .SAIDA(\memória_1x8_flip_flop_jk_4_saida ));
  Multiplexer #(.select(2), .width(8)) multiplexer_1 (
    .in0(\memória_1x8_flip_flop_jk_1_saida ), .in1(\memória_1x8_flip_flop_jk_2_saida ),
    .in2(\memória_1x8_flip_flop_jk_3_saida ), .in3(\memória_1x8_flip_flop_jk_4_saida ), .out(SAIDA),
    .sel(ADDR));

  // Notes on the sheet:
  //   Memória 4x8
  //   flip-flop JK
  //   Marcos Felipe Martins Silva-415719
endmodule
