// Logisim project Memoria.circ as structural Verilog
module Memoria_Ram_1x4b (
  input  Addr,
  input  W,
  input  Clock,
  input  B1,
  input  B2,
  input  B3,
  input  B4,
  input  R,
  input  Clear,
  output out1,
  output out2,
  output out3,
  output out4
);

  wire and_1_out, and_2_out, and_3_out, and_4_out, and_5_out, controlled_buffer_1_out,
       controlled_buffer_2_out, controlled_buffer_3_out, controlled_buffer_4_out, d_ff_1_q, d_ff_2_q,
       d_ff_3_q, d_ff_4_q, not_1_out;

  and and_1 (and_1_out, W, B1);
  assign controlled_buffer_1_out = Addr ? and_1_out : 1'bz;  // Controlled_Buffer controlled_buffer_1
  and and_2 (and_2_out, W, B2);
  assign controlled_buffer_2_out = Addr ? and_2_out : 1'bz;  // Controlled_Buffer controlled_buffer_2
  and and_3 (and_3_out, W, B3);
  assign controlled_buffer_3_out = Addr ? and_3_out : 1'bz;  // Controlled_Buffer controlled_buffer_3
  and and_4 (and_4_out, W, B4);
  assign controlled_buffer_4_out = Addr ? and_4_out : 1'bz;  // Controlled_Buffer controlled_buffer_4
  not not_1 (not_1_out, Clock);
  D_Flip_Flop #(.trigger("rising")) d_ff_1 (
    .clk(Clock), .D(controlled_buffer_1_out), .Q(d_ff_1_q), .reset(Clear));  // open: Qn, preset, en
  D_Flip_Flop #(.trigger("rising")) d_ff_2 (
    .clk(Clock), .D(controlled_buffer_2_out), .Q(d_ff_2_q), .reset(Clear));  // open: Qn, preset, en
  D_Flip_Flop #(.trigger("rising")) d_ff_3 (
    .clk(Clock), .D(controlled_buffer_3_out), .Q(d_ff_3_q), .reset(Clear));  // open: Qn, preset, en
  D_Flip_Flop #(.trigger("rising")) d_ff_4 (
    .clk(Clock), .D(controlled_buffer_4_out), .Q(d_ff_4_q), .reset(Clear));  // open: Qn, preset, en
  and and_5 (and_5_out, not_1_out, Addr, R);
  assign out1 = and_5_out ? d_ff_1_q : 1'bz;  // Controlled_Buffer controlled_buffer_5
  assign out2 = and_5_out ? d_ff_2_q : 1'bz;  // Controlled_Buffer controlled_buffer_6
  assign out3 = and_5_out ? d_ff_3_q : 1'bz;  // Controlled_Buffer controlled_buffer_7
  assign out4 = and_5_out ? d_ff_4_q : 1'bz;  // Controlled_Buffer controlled_buffer_8

  // Notes on the sheet:
  //   Henrique Carvalho Parreira
endmodule

module Memoria_Ram_1x8 (
  input  Addr,
  input  W,
  input  Clock,
  input  B1,
  input  B2,
  input  B3,
  input  B4,
  input  B5,
  input  B6,
  input  B7,
  input  B8,
  input  R,
  input  Clear,
  output out_14,
  output out_15,
  output out_16,
  output out_17,
  output out_18,
  output out_19,
  output out_20,
  output out_21
);

  Memoria_Ram_1x4b memoria_ram_1x4b_1 (
    .Addr(Addr), .W(W), .Clock(Clock), .B1(B1), .B2(B2), .B3(B3), .B4(B4), .R(R), .Clear(Clear),
    .out1(out_14), .out2(out_15), .out3(out_16), .out4(out_17));
  Memoria_Ram_1x4b memoria_ram_1x4b_2 (
    .Addr(Addr), .W(W), .Clock(Clock), .B1(B5), .B2(B6), .B3(B7), .B4(B8), .R(R), .Clear(Clear),
    .out1(out_18), .out2(out_19), .out3(out_20), .out4(out_21));

  // Notes on the sheet:
  //   Henrique Carvalho Parreira
endmodule

module Memoria_Ram_4X8 (
  input  W,
  input  Clock,
  input  R,
  input  Clear,
  input  [7:0] Entrada,
  input  [1:0] in_6,
  output [7:0] Saida
);

  wire decoder_1_out0, decoder_1_out1, decoder_1_out2, decoder_1_out3;
  wire [7:0] demultiplexer_1_out0, demultiplexer_1_out1, demultiplexer_1_out2, demultiplexer_1_out3,
       memoria_ram_1x8_1_out_14, memoria_ram_1x8_2_out_14, memoria_ram_1x8_3_out_14, memoria_ram_1x8_4_out_14;

  Decoder #(.select(2), .tristate("false")) decoder_1 (
    .out0(decoder_1_out0), .out1(decoder_1_out1), .out2(decoder_1_out2), .out3(decoder_1_out3), .sel(in_6));
  Demultiplexer #(.select(2), .width(8), .tristate("false")) demultiplexer_1 (
    .out0(demultiplexer_1_out0), .out1(demultiplexer_1_out1), .out2(demultiplexer_1_out2),
    .out3(demultiplexer_1_out3), .in(Entrada), .sel(in_6));
  Memoria_Ram_1x8 memoria_ram_1x8_1 (
    .Addr(decoder_1_out0), .W(W), .Clock(Clock), .B1(demultiplexer_1_out0[0]), .B2(demultiplexer_1_out0[1]),
    .B3(demultiplexer_1_out0[2]), .B4(demultiplexer_1_out0[3]), .B5(demultiplexer_1_out0[4]),
    .B6(demultiplexer_1_out0[5]), .B7(demultiplexer_1_out0[6]), .B8(demultiplexer_1_out0[7]), .R(R),
    .Clear(Clear), .out_14(memoria_ram_1x8_1_out_14[0]), .out_15(memoria_ram_1x8_1_out_14[1]),
    .out_16(memoria_ram_1x8_1_out_14[2]), .out_17(memoria_ram_1x8_1_out_14[3]),
    .out_18(memoria_ram_1x8_1_out_14[4]), .out_19(memoria_ram_1x8_1_out_14[5]),
    .out_20(memoria_ram_1x8_1_out_14[6]), .out_21(memoria_ram_1x8_1_out_14[7]));
  Memoria_Ram_1x8 memoria_ram_1x8_2 (
    .Addr(decoder_1_out1), .W(W), .Clock(Clock), .B1(demultiplexer_1_out1[0]), .B2(demultiplexer_1_out1[1]),
    .B3(demultiplexer_1_out1[2]), .B4(demultiplexer_1_out1[3]), .B5(demultiplexer_1_out1[4]),
    .B6(demultiplexer_1_out1[5]), .B7(demultiplexer_1_out1[6]), .B8(demultiplexer_1_out1[7]), .R(R),
    .Clear(Clear), .out_14(memoria_ram_1x8_2_out_14[0]), .out_15(memoria_ram_1x8_2_out_14[1]),
    .out_16(memoria_ram_1x8_2_out_14[2]), .out_17(memoria_ram_1x8_2_out_14[3]),
    .out_18(memoria_ram_1x8_2_out_14[4]), .out_19(memoria_ram_1x8_2_out_14[5]),
    .out_20(memoria_ram_1x8_2_out_14[6]), .out_21(memoria_ram_1x8_2_out_14[7]));
  Memoria_Ram_1x8 memoria_ram_1x8_3 (
    .Addr(decoder_1_out2), .W(W), .Clock(Clock), .B1(demultiplexer_1_out2[0]), .B2(demultiplexer_1_out2[1]),
    .B3(demultiplexer_1_out2[2]), .B4(demultiplexer_1_out2[3]), .B5(demultiplexer_1_out2[4]),
    .B6(demultiplexer_1_out2[5]), .B7(demultiplexer_1_out2[6]), .B8(demultiplexer_1_out2[7]), .R(R),
    .Clear(Clear), .out_14(memoria_ram_1x8_3_out_14[0]), .out_15(memoria_ram_1x8_3_out_14[1]),
    .out_16(memoria_ram_1x8_3_out_14[2]), .out_17(memoria_ram_1x8_3_out_14[3]),
    .out_18(memoria_ram_1x8_3_out_14[4]), .out_19(memoria_ram_1x8_3_out_14[5]),
    .out_20(memoria_ram_1x8_3_out_14[6]), .out_21(memoria_ram_1x8_3_out_14[7]));
  Memoria_Ram_1x8 memoria_ram_1x8_4 (
    .Addr(decoder_1_out3), .W(W), .Clock(Clock), .B1(demultiplexer_1_out3[0]), .B2(demultiplexer_1_out3[1]),
    .B3(demultiplexer_1_out3[2]), .B4(demultiplexer_1_out3[3]), .B5(demultiplexer_1_out3[4]),
    .B6(demultiplexer_1_out3[5]), .B7(demultiplexer_1_out3[6]), .B8(demultiplexer_1_out3[7]), .R(R),
    .Clear(Clear), .out_14(memoria_ram_1x8_4_out_14[0]), .out_15(memoria_ram_1x8_4_out_14[1]),
    .out_16(memoria_ram_1x8_4_out_14[2]), .out_17(memoria_ram_1x8_4_out_14[3]),
    .out_18(memoria_ram_1x8_4_out_14[4]), .out_19(memoria_ram_1x8_4_out_14[5]),
    .out_20(memoria_ram_1x8_4_out_14[6]), .out_21(memoria_ram_1x8_4_out_14[7]));
  Multiplexer #(.select(2), .width(8)) multiplexer_1 (
    .in0(memoria_ram_1x8_1_out_14), .in1(memoria_ram_1x8_2_out_14), .in2(memoria_ram_1x8_3_out_14),
    .in3(memoria_ram_1x8_4_out_14), .out(Saida), .sel(in_6));

  // Notes on the sheet:
  //   Henrique Carvalho Parreira - 347133
endmodule
