// Logisim project Prova1Tabela.circ as structural Verilog: 4 circuits, main circuit main
module main (
  input  a,
  input  b,
  input  c,
  input  d,
  output [2:0] S
);

  S0 s0_1 (.a(a), .b(b), .c(c), .d(d), .S0(S[0]));
  S1 s1_1 (.a(a), .b(b), .c(c), .d(d), .S1(S[1]));
  S2 s2_1 (.a(a), .b(b), .c(c), .d(d), .S2(S[2]));
endmodule

module S0 (
  input  a,
  input  b,
  input  c,
  input  d,
  output S0
);

  wire xnor_1_out, xnor_2_out;

  xnor xnor_1 (xnor_1_out, a, b);
  xnor xnor_2 (xnor_2_out, c, d);
  xor xor_1 (S0, xnor_1_out, xnor_2_out);
endmodule

module S1 (
  input  a,
  input  b,
  input  c,
  input  d,
  output S1
);

  wire and_1_out, and_2_out, and_3_out, and_4_out, xor_1_out, xor_2_out, xor_3_out, xor_4_out;

  xor xor_1 (xor_1_out, a, c);
  xor xor_2 (xor_2_out, b, c);
  xor xor_3 (xor_3_out, a, b);
  xor xor_4 (xor_4_out, b, d);
  and and_1 (and_1_out, d, xor_1_out);
  and and_2 (and_2_out, d, xor_2_out);
  and and_3 (and_3_out, xor_3_out, c);
  and and_4 (and_4_out, xor_4_out, a);
  or or_1 (S1, and_1_out, and_2_out, and_3_out, and_4_out);
endmodule

module S2 (
  input  a,
  input  b,
  input  c,
  input  d,
  output S2
);

  and and_1 (S2, a, b, c, d);
endmodule
