// Logisim project Prova.circ as structural Verilog: 5 circuits, main circuit s0MinTermo
module s0MinTermo (
  input  a,
  input  b,
  input  c,
  input  d,
  output s0
);

  wire and_1_out, and_2_out, and_3_out, and_4_out, and_5_out, and_6_out, and_7_out, and_8_out, not_1_out,
       not_2_out, not_3_out, not_4_out;

  not not_1 (not_1_out, a);
  not not_2 (not_2_out, b);
  not not_3 (not_3_out, c);
  not not_4 (not_4_out, d);
  and and_1 (and_1_out, not_1_out, not_2_out, not_3_out, d);
  and and_2 (and_2_out, not_1_out, not_2_out, c, not_4_out);
  and and_3 (and_3_out, not_1_out, b, not_3_out, not_4_out);
  and and_4 (and_4_out, not_1_out, b, c, d);
  and and_5 (and_5_out, a, not_2_out, not_3_out, not_4_out);
  and and_6 (and_6_out, a, not_2_out, c, d);
  and and_7 (and_7_out, a, b, not_4_out, d);
  and and_8 (and_8_out, a, b, c, not_4_out);
  or or_1 (s0, and_1_out, and_2_out, and_3_out, and_4_out, and_5_out, and_6_out, and_7_out, and_8_out);
endmodule

module s0MaxTermo (
  input  a,
  input  b,
  input  c,
  input  d,
  output s0
);

  wire not_1_out, not_2_out, not_3_out, not_4_out, not_5_out, not_6_out, not_7_out, not_8_out, not_9_out,
       not_10_out, not_11_out, not_12_out, not_13_out, not_14_out, not_15_out, not_16_out, or_1_out,
       or_2_out, or_3_out, or_4_out, or_5_out, or_6_out, or_7_out, or_8_out;

  not not_1 (not_1_out, c);
  not not_2 (not_2_out, b);
  not not_3 (not_3_out, d);
  not not_4 (not_4_out, b);
  not not_5 (not_5_out, a);
  not not_6 (not_6_out, d);
  not not_7 (not_7_out, a);
  not not_8 (not_8_out, c);
  not not_9 (not_9_out, a);
  not not_10 (not_10_out, a);
  not not_11 (not_11_out, d);
  not not_12 (not_12_out, c);
  not not_13 (not_13_out, b);
  not not_14 (not_14_out, b);
  not not_15 (not_15_out, c);
  not not_16 (not_16_out, d);
  or or_1 (or_1_out, a, b, c, d);
  or or_2 (or_2_out, a, b, not_1_out, not_11_out);
  or or_3 (or_3_out, a, not_2_out, c, not_3_out);
  or or_4 (or_4_out, a, not_4_out, not_12_out, d);
  or or_5 (or_5_out, not_5_out, b, c, not_6_out);
  or or_6 (or_6_out, not_7_out, b, not_8_out, d);
  or or_7 (or_7_out, not_9_out, not_13_out, c, d);
  or or_8 (or_8_out, not_10_out, not_14_out, not_15_out, not_16_out);
  and and_1 (s0, or_1_out, or_2_out, or_3_out, or_4_out, or_6_out, or_7_out, or_8_out);
endmodule

module s0simplificada (
  input  a,
  input  b,
  input  c,
  input  d,
  output s0
);

  wire and_1_out, and_2_out, and_3_out, and_4_out, and_5_out, and_6_out, and_7_out, not_1_out, not_2_out,
       not_3_out, not_4_out, not_5_out, not_6_out, not_7_out, not_8_out, not_9_out, not_10_out, not_11_out,
       not_12_out, not_13_out, not_14_out;

  not not_1 (not_1_out, d);
  not not_2 (not_2_out, b);
  not not_3 (not_3_out, d);
  not not_4 (not_4_out, a);
  not not_5 (not_5_out, c);
  not not_6 (not_6_out, b);
  not not_7 (not_7_out, a);
  not not_8 (not_8_out, a);
  not not_9 (not_9_out, d);
  not not_10 (not_10_out, c);
  not not_11 (not_11_out, b);
  not not_12 (not_12_out, c);
  not not_13 (not_13_out, c);
  not not_14 (not_14_out, d);
  and and_1 (and_1_out, a, c, not_1_out);
  and and_2 (and_2_out, not_2_out, c, not_3_out);
  and and_3 (and_3_out, not_4_out, b, not_9_out);
  and and_4 (and_4_out, a, not_6_out, not_10_out, not_14_out);
  and and_5 (and_5_out, not_7_out, not_11_out, not_12_out, d);
  and and_6 (and_6_out, a, b, not_13_out, d);
  and and_7 (and_7_out, not_8_out, b, c, d);
  or or_1 (s0, and_1_out, and_2_out, and_3_out, and_4_out, and_5_out, and_6_out, and_7_out);
endmodule

module s0simplificadaporAlgebra (
  input  a,
  input  b,
  input  c,
  input  d,
  output s0
);

  wire xnor_1_out, xnor_2_out;

  xnor xnor_1 (xnor_1_out, a, b);
  xnor xnor_2 (xnor_2_out, c, d);
  or or_1 (s0, xnor_1_out, xnor_2_out);
endmodule

module s1quine (
  input  a,
  input  b,
  input  c,
  input  d,
  output s1
);

  wire and_1_out, and_2_out, and_3_out, and_4_out, and_5_out, and_6_out, not_1_out, not_2_out, not_3_out,
       not_4_out, not_5_out, not_6_out;

  not not_1 (not_1_out, b);
  not not_2 (not_2_out, a);
  not not_3 (not_3_out, d);
  not not_4 (not_4_out, b);
  not not_5 (not_5_out, b);
  not not_6 (not_6_out, d);
  and and_1 (and_1_out, not_1_out, c, d);
  and and_2 (and_2_out, not_2_out, b, d);
  and and_3 (and_3_out, b, c, not_3_out);
  and and_4 (and_4_out, a, not_4_out, d);
  and and_5 (and_5_out, a, not_5_out, c);
  and and_6 (and_6_out, a, b, not_6_out);
  or or_1 (s1, and_1_out, and_2_out, and_3_out, and_5_out, and_6_out, and_4_out);
endmodule
