// Logisim project circuito.circ as structural Verilog: 8 circuits, main circuit Letra B
module Letra_B (
  input  A,
  input  B,
  input  C,
  input  D,
  output s
);

  wire and_1_out, and_2_out, and_3_out, and_4_out, and_5_out, and_6_out, and_7_out, and_8_out, not_1_out,
       not_2_out, not_3_out, not_4_out, not_5_out, not_6_out, not_7_out, not_8_out, not_9_out, not_10_out,
       not_11_out, not_12_out, not_13_out, not_14_out, not_15_out, not_16_out;

  not not_1 (not_1_out, A);
  not not_2 (not_2_out, B);
  not not_3 (not_3_out, C);
  not not_4 (not_4_out, A);
  not not_5 (not_5_out, B);
  not not_6 (not_6_out, D);
  not not_7 (not_7_out, A);
  not not_8 (not_8_out, C);
  not not_9 (not_9_out, D);
  not not_10 (not_10_out, A);
  not not_11 (not_11_out, B);
  not not_12 (not_12_out, C);
  not not_13 (not_13_out, D);
  not not_14 (not_14_out, B);
  not not_15 (not_15_out, C);
  not not_16 (not_16_out, D);
  and and_1 (and_1_out, not_1_out, D, not_2_out, not_3_out);
  and and_2 (and_2_out, not_4_out, C, not_5_out, not_6_out);
  and and_3 (and_3_out, not_7_out, B, not_8_out, not_9_out);
  and and_4 (and_4_out, not_10_out, B, C, D);
  and and_5 (and_5_out, not_11_out, A, not_12_out, not_13_out);
  and and_6 (and_6_out, not_14_out, A, C, D);
  and and_7 (and_7_out, not_15_out, A, B, D);
  and and_8 (and_8_out, not_16_out, A, B, C);
  or or_1 (s, and_1_out, and_2_out, and_3_out, and_4_out, and_5_out, and_6_out, and_7_out, and_8_out);

  // Notes on the sheet:
  //   Paulo Henrique de Almeida Amorim
  //   412765
endmodule

module Letra_C (
  input  A,
  input  B,
  input  C,
  input  D,
  output s
);

  wire and_1_out, and_2_out, and_3_out, and_4_out, and_5_out, and_6_out, and_7_out, and_8_out, and_9_out,
       and_10_out, not_1_out, not_2_out, not_3_out, not_4_out, not_5_out, not_6_out, not_7_out, not_8_out,
       not_9_out, not_10_out, not_11_out, not_12_out, not_13_out, not_14_out, not_15_out, not_16_out;

  not not_1 (not_1_out, A);
  not not_2 (not_2_out, B);
  not not_3 (not_3_out, A);
  not not_4 (not_4_out, C);
  not not_5 (not_5_out, A);
  not not_6 (not_6_out, D);
  not not_7 (not_7_out, A);
  not not_8 (not_8_out, B);
  not not_9 (not_9_out, C);
  not not_10 (not_10_out, B);
  not not_11 (not_11_out, D);
  not not_12 (not_12_out, B);
  not not_13 (not_13_out, C);
  not not_14 (not_14_out, D);
  not not_15 (not_15_out, C);
  not not_16 (not_16_out, D);
  and and_1 (and_1_out, not_1_out, not_2_out, C, D);
  and and_2 (and_2_out, not_3_out, not_4_out, B, D);
  and and_3 (and_3_out, not_5_out, not_6_out, B, C);
  and and_4 (and_4_out, not_7_out, B, C, D);
  and and_5 (and_5_out, not_8_out, not_9_out, A, D);
  and and_6 (and_6_out, not_10_out, not_11_out, A, C);
  and and_7 (and_7_out, not_12_out, A, C, D);
  and and_8 (and_8_out, not_13_out, not_14_out, A, B);
  and and_9 (and_9_out, not_15_out, A, B, D);
  and and_10 (and_10_out, not_16_out, A, B, C);
  or or_1 (s, and_1_out, and_2_out, and_3_out, and_4_out, and_5_out, and_6_out, and_7_out, and_8_out, and_9_out, and_10_out);

  // Notes on the sheet:
  //   Paulo Henrique de Almeida Amorim
  //   412765
endmodule

module Letra_D (
  input  A,
  input  B,
  input  C,
  input  D,
  output s
);

  wire not_1_out, not_2_out, not_3_out, not_4_out, not_5_out, not_6_out, not_7_out, not_8_out, not_9_out,
       not_10_out, not_11_out, not_12_out, not_13_out, not_14_out, not_15_out, not_16_out, or_1_out,
       or_2_out, or_3_out, or_4_out, or_5_out, or_6_out, or_7_out, or_8_out;

  not not_1 (not_1_out, C);
  not not_2 (not_2_out, D);
  not not_3 (not_3_out, B);
  not not_4 (not_4_out, D);
  not not_5 (not_5_out, B);
  not not_6 (not_6_out, C);
  not not_7 (not_7_out, A);
  not not_8 (not_8_out, D);
  not not_9 (not_9_out, A);
  not not_10 (not_10_out, C);
  not not_11 (not_11_out, A);
  not not_12 (not_12_out, B);
  not not_13 (not_13_out, A);
  not not_14 (not_14_out, C);
  or or_1 (or_1_out, A, B, C, D);
  or or_2 (or_2_out, not_1_out, not_2_out, A, B);
  or or_3 (or_3_out, not_3_out, not_4_out, A, C);
  or or_4 (or_4_out, not_5_out, not_6_out, A, D);
  or or_5 (or_5_out, not_7_out, not_8_out, B, C);
  or or_6 (or_6_out, not_9_out, not_10_out, B, D);
  or or_7 (or_7_out, not_11_out, not_12_out, C, D);
  not not_15 (not_15_out, B);
  not not_16 (not_16_out, D);
  or or_8 (or_8_out, not_13_out, not_15_out, not_14_out, not_16_out);
  and and_1 (s, or_1_out, or_2_out, or_3_out, or_4_out, or_5_out, or_6_out, or_7_out, or_8_out);

  // Notes on the sheet:
  //   Paulo Henrique de Almeida Amorim
  //   412765
endmodule

module Letra_E (
  input  A,
  input  B,
  input  C,
  input  D,
  output s
);

  wire and_1_out, and_2_out, and_3_out, and_4_out, and_5_out, and_6_out, and_7_out, and_8_out, not_1_out,
       not_2_out, not_3_out, not_4_out, not_5_out, not_6_out, not_7_out, not_8_out, not_9_out, not_10_out,
       not_11_out, not_12_out, not_13_out, not_14_out, not_15_out, not_16_out;

  not not_1 (not_1_out, A);
  not not_2 (not_2_out, B);
  not not_3 (not_3_out, C);
  not not_4 (not_4_out, A);
  not not_5 (not_5_out, B);
  not not_6 (not_6_out, D);
  not not_7 (not_7_out, A);
  not not_8 (not_8_out, C);
  not not_9 (not_9_out, D);
  not not_10 (not_10_out, B);
  not not_11 (not_11_out, C);
  not not_12 (not_12_out, D);
  not not_13 (not_13_out, B);
  not not_14 (not_14_out, C);
  not not_15 (not_15_out, A);
  not not_16 (not_16_out, D);
  and and_1 (and_1_out, not_1_out, D, not_2_out, not_3_out);
  and and_2 (and_2_out, not_4_out, C, not_5_out, not_6_out);
  and and_3 (and_3_out, not_7_out, B, not_8_out, not_9_out);
  and and_4 (and_4_out, not_10_out, A, not_11_out, not_12_out);
  and and_5 (and_5_out, not_13_out, A, C, D);
  and and_6 (and_6_out, not_14_out, A, B, D);
  and and_7 (and_7_out, not_15_out, B, C, D);
  and and_8 (and_8_out, not_16_out, A, B, C);
  or or_1 (s, and_1_out, and_2_out, and_3_out, and_4_out, and_5_out, and_6_out, and_7_out, and_8_out);

  // Notes on the sheet:
  //   Paulo Henrique de Almeida Amorim
  //   412765
endmodule

module Letra_F (
  input  A,
  input  B,
  input  C,
  input  D,
  output s
);

  wire and_1_out, and_2_out, and_3_out, and_4_out, not_1_out, not_2_out, not_3_out, not_4_out, xor_1_out,
       xor_2_out, xor_3_out, xor_4_out;

  xor xor_1 (xor_1_out, C, D);
  xor xor_2 (xor_2_out, A, C);
  xor xor_3 (xor_3_out, A, B);
  xor xor_4 (xor_4_out, B, D);
  not not_1 (not_1_out, A);
  not not_2 (not_2_out, B);
  not not_3 (not_3_out, C);
  not not_4 (not_4_out, D);
  and and_1 (and_1_out, xor_1_out, not_1_out, not_2_out);
  and and_2 (and_2_out, xor_2_out, B, D);
  and and_3 (and_3_out, xor_3_out, not_3_out, not_4_out);
  and and_4 (and_4_out, xor_4_out, C, A);
  or or_1 (s, and_1_out, and_2_out, and_3_out, and_4_out);

  // Notes on the sheet:
  //   Paulo Henrique de Almeida Amorim
  //   412765
endmodule

module Letra_G (
  input  A,
  input  B,
  input  C,
  input  D,
  output s
);

  wire and_1_out, and_2_out, and_3_out, and_4_out, and_5_out, and_6_out, and_7_out, and_8_out, and_9_out,
       not_1_out, not_2_out, not_3_out, not_4_out, not_5_out, not_6_out, not_7_out, not_8_out, not_9_out;

  not not_1 (not_1_out, A);
  not not_2 (not_2_out, B);
  not not_3 (not_3_out, C);
  not not_4 (not_4_out, A);
  not not_5 (not_5_out, B);
  not not_6 (not_6_out, C);
  not not_7 (not_7_out, B);
  not not_8 (not_8_out, C);
  not not_9 (not_9_out, D);
  and and_1 (and_1_out, not_1_out, C, D);
  and and_2 (and_2_out, not_2_out, C, D);
  and and_3 (and_3_out, not_3_out, B, D);
  and and_4 (and_4_out, not_4_out, B, C);
  and and_5 (and_5_out, not_5_out, A, D);
  and and_6 (and_6_out, not_6_out, A, D);
  and and_7 (and_7_out, not_7_out, A, C);
  and and_8 (and_8_out, not_8_out, A, B);
  and and_9 (and_9_out, not_9_out, A, B);
  or or_1 (s, and_1_out, and_2_out, and_3_out, and_4_out, and_5_out, and_6_out, and_7_out, and_8_out, and_9_out);

  // Notes on the sheet:
  //   Paulo Henrique de Almeida Amorim
  //   412765
endmodule

module Letra_I (
  input  A,
  input  B,
  input  C,
  input  D,
  output s
);

  wire and_1_out, and_2_out, and_3_out, and_4_out, xor_1_out, xor_2_out, xor_3_out, xor_4_out;

  xor xor_1 (xor_1_out, A, C);
  xor xor_2 (xor_2_out, B, C);
  xor xor_3 (xor_3_out, A, B);
  xor xor_4 (xor_4_out, B, D);
  and and_1 (and_1_out, xor_1_out, D);
  and and_2 (and_2_out, xor_2_out, D);
  and and_3 (and_3_out, xor_3_out, C);
  and and_4 (and_4_out, xor_4_out, A);
  or or_1 (s, and_1_out, and_2_out, and_3_out, and_4_out);

  // Notes on the sheet:
  //   Paulo Henrique de Almeida Amorim
  //   412765
endmodule

module Letra_J (
  input  A,
  input  B,
  input  C,
  input  D,
  output s
);

  and and_1 (s, A, B, C, D);

  // Notes on the sheet:
  //   Paulo Henrique de Almeida Amorim
  //   412765
endmodule
