// Logisim project prova_circuito.circ as structural Verilog: 8 circuits, main circuit s0mintermos
module s0mintermos (
  input  a,
  input  b,
  input  c,
  input  d,
  output s0_mintermos
);

  wire and_1_out, and_3_out, and_4_out, and_5_out, and_6_out, and_7_out, and_8_out, not_1_out, not_2_out,
       not_3_out, not_4_out, not_5_out, not_6_out, not_7_out;

  not not_1 (not_1_out, a);
  not not_2 (not_2_out, b);
  not not_3 (not_3_out, c);
  not not_4 (not_4_out, b);
  not not_5 (not_5_out, c);
  not not_6 (not_6_out, d);
  not not_7 (not_7_out, d);
  and and_1 (and_1_out, d, not_3_out, not_2_out, not_1_out);
  and and_2 (and_1_out, not_1_out, not_2_out, c, not_7_out);
  and and_3 (and_3_out, b, not_1_out, not_3_out, not_7_out);
  and and_4 (and_4_out, d, c, b, not_1_out);
  and and_5 (and_5_out, a, not_4_out, not_6_out, not_5_out);
  and and_6 (and_6_out, a, not_4_out, c, c);
  and and_7 (and_7_out, not_5_out, d, a, b);
  and and_8 (and_8_out, not_6_out, c, a, b);
  or or_1 (s0_mintermos, and_6_out, and_1_out, and_5_out, and_4_out, and_7_out, and_8_out, and_1_out, and_3_out);

  // Notes on the sheet:
  //   Silvino Henrique Santos de Souza - 412773
endmodule

module s1mintermos (
  input  a,
  input  b,
  input  c,
  input  d,
  output s1_mintermos
);

  wire and_1_out, and_2_out, and_3_out, and_4_out, and_5_out, and_6_out, and_7_out, and_8_out, and_9_out,
       and_10_out, not_1_out, not_2_out, not_3_out, not_4_out, not_5_out, not_6_out, not_7_out, not_8_out;

  not not_1 (not_1_out, a);
  not not_2 (not_2_out, a);
  not not_3 (not_3_out, b);
  not not_4 (not_4_out, b);
  not not_5 (not_5_out, c);
  not not_6 (not_6_out, c);
  not not_7 (not_7_out, d);
  not not_8 (not_8_out, d);
  and and_1 (and_1_out, not_1_out, not_3_out, c, d);
  and and_2 (and_2_out, not_1_out, d, not_6_out, b);
  and and_3 (and_3_out, not_1_out, b, c, not_7_out);
  and and_4 (and_4_out, not_2_out, d, c, b);
  and and_5 (and_5_out, not_3_out, not_6_out, a, d);
  and and_6 (and_6_out, not_7_out, not_4_out, a, c);
  and and_7 (and_7_out, not_4_out, a, c, d);
  and and_8 (and_8_out, not_5_out, a, b, not_8_out);
  and and_9 (and_9_out, not_5_out, d, b, a);
  and and_10 (and_10_out, not_8_out, c, b, a);
  or or_1 (s1_mintermos, and_1_out, and_2_out, and_3_out, and_4_out, and_5_out, and_6_out, and_7_out, and_8_out, and_9_out, and_10_out);

  // Notes on the sheet:
  //   Silvino Henrique Santos de Souza - 412773
endmodule

module s0maxtermos (
  input  a,
  input  b,
  input  c,
  input  d,
  output s0_maxtermos
);

  wire not_1_out, not_2_out, not_3_out, not_4_out, not_5_out, not_6_out, not_7_out, not_8_out, or_1_out,
       or_2_out, or_3_out, or_4_out, or_5_out, or_6_out, or_7_out, or_8_out;

  not not_1 (not_1_out, a);
  not not_2 (not_2_out, a);
  not not_3 (not_3_out, b);
  not not_4 (not_4_out, b);
  not not_5 (not_5_out, c);
  not not_6 (not_6_out, c);
  not not_7 (not_7_out, d);
  not not_8 (not_8_out, d);
  or or_1 (or_1_out, a, b, c, d);
  or or_2 (or_2_out, not_5_out, b, not_7_out, a);
  or or_3 (or_3_out, not_3_out, not_7_out, a, c);
  or or_4 (or_4_out, not_3_out, d, not_5_out, a);
  or or_5 (or_5_out, not_1_out, c, not_7_out, b);
  or or_6 (or_6_out, not_1_out, not_5_out, d, b);
  or or_7 (or_7_out, not_1_out, d, not_3_out, c);
  or or_8 (or_8_out, not_2_out, not_4_out, not_8_out, not_6_out);
  and and_1 (s0_maxtermos, or_1_out, or_2_out, or_3_out, or_4_out, or_5_out, or_7_out, or_6_out, or_8_out);

  // Notes on the sheet:
  //   Silvino Henrique Santos de Souza - 412773
endmodule

module s0Karnaugh (
  input  a,
  input  b,
  input  c,
  input  d,
  output s0_Karnaugh
);

  wire and_1_out, and_2_out, and_3_out, and_4_out, and_5_out, and_6_out, and_7_out, and_8_out, not_1_out,
       not_2_out, not_3_out, not_4_out, not_5_out, not_6_out, not_7_out, not_8_out;

  not not_1 (not_1_out, a);
  not not_2 (not_2_out, b);
  not not_3 (not_3_out, c);
  not not_4 (not_4_out, d);
  not not_5 (not_5_out, a);
  not not_6 (not_6_out, b);
  not not_7 (not_7_out, c);
  not not_8 (not_8_out, d);
  and and_1 (and_1_out, not_5_out, not_6_out, not_7_out, d);
  and and_2 (and_2_out, not_5_out, not_6_out, not_8_out, c);
  and and_3 (and_3_out, not_5_out, not_7_out, not_8_out, b);
  and and_4 (and_4_out, not_2_out, a, not_3_out);
  and and_5 (and_5_out, a, not_2_out, c, d);
  and and_6 (and_6_out, not_3_out, d, a, b);
  and and_7 (and_7_out, not_1_out, d, b, c);
  and and_8 (and_8_out, not_4_out, a, b, c);
  or or_1 (s0_Karnaugh, and_1_out, and_2_out, and_3_out, and_4_out, and_5_out, and_6_out, and_7_out, and_8_out);

  // Notes on the sheet:
  //   Silvino Henrique Santos de Souza - 412773
endmodule

module s0algebra (
  input  a,
  input  b,
  input  c,
  input  d,
  output s0_algebra
);

  wire and_1_out, and_2_out, and_3_out, and_4_out, not_1_out, not_2_out, not_3_out, not_4_out, xor_1_out,
       xor_2_out, xor_3_out, xor_4_out;

  not not_1 (not_1_out, a);
  not not_2 (not_2_out, d);
  xor xor_1 (xor_1_out, c, d);
  xor xor_2 (xor_2_out, a, c);
  xor xor_3 (xor_3_out, b, a);
  xor xor_4 (xor_4_out, b, d);
  not not_3 (not_3_out, b);
  and and_1 (and_1_out, xor_2_out, b, d);
  not not_4 (not_4_out, c);
  and and_2 (and_2_out, xor_4_out, a, c);
  and and_3 (and_3_out, xor_1_out, not_1_out, not_3_out);
  and and_4 (and_4_out, xor_3_out, not_4_out, not_2_out);
  or or_1 (s0_algebra, and_3_out, and_1_out, and_4_out, and_2_out);

  // Notes on the sheet:
  //   Silvino Henrique Santos de Souza - 412773
endmodule

module s1algebra (
  input  a,
  input  b,
  input  c,
  input  d,
  output s1_algebra
);

  wire and_1_out, and_2_out, and_3_out, and_4_out, xor_1_out, xor_2_out, xor_3_out, xor_4_out;

  xor xor_1 (xor_1_out, a, c);
  xor xor_2 (xor_2_out, b, c);
  xor xor_3 (xor_3_out, a, b);
  xor xor_4 (xor_4_out, b, d);
  and and_1 (and_1_out, xor_2_out, d);
  and and_2 (and_2_out, xor_3_out, c);
  and and_3 (and_3_out, xor_4_out, a);
  and and_4 (and_4_out, xor_1_out, d);
  or or_1 (s1_algebra, and_4_out, and_1_out, and_2_out, and_3_out);

  // Notes on the sheet:
  //   t2
  //   t3
  //   t4
  //   t1
  //   Silvino Henrique Santos de Souza - 412773
  //   t6
  //   t7
  //   t8
  //   t5
endmodule

module s1Quine (
  input  a,
  input  b,
  input  c,
  input  d,
  output s1_Quine
);

  wire and_1_out, and_2_out, and_3_out, and_4_out, and_5_out, and_6_out, and_7_out, and_8_out, and_9_out,
       not_1_out, not_2_out, not_3_out, not_4_out, not_5_out, not_6_out;

  not not_1 (not_1_out, a);
  not not_2 (not_2_out, b);
  not not_3 (not_3_out, b);
  not not_4 (not_4_out, c);
  not not_5 (not_5_out, c);
  not not_6 (not_6_out, d);
  and and_1 (and_1_out, not_1_out, c, d);
  and and_2 (and_2_out, not_3_out, c, d);
  and and_3 (and_3_out, not_4_out, b, d);
  and and_4 (and_4_out, not_1_out, b, c);
  and and_5 (and_5_out, not_3_out, a, d);
  and and_6 (and_6_out, not_4_out, a, d);
  and and_7 (and_7_out, not_2_out, a, c);
  and and_8 (and_8_out, not_5_out, a, a, b);
  and and_9 (and_9_out, not_6_out, a, b);
  or or_1 (s1_Quine, and_1_out, and_2_out, and_3_out, and_4_out, and_5_out, and_6_out, and_7_out, and_8_out, and_9_out);

  // Notes on the sheet:
  //   Silvino Henrique Santos de Souza - 412773
endmodule

module s2 (
  input  a,
  input  b,
  input  c,
  input  d,
  output s2_ultimo_exercicio
);

  and and_1 (s2_ultimo_exercicio, a, b, c, d);

  // Notes on the sheet:
  //   Silvino Henrique Santos de Souza - 412773
endmodule
