// Logisim project prova01-b.circ as structural Verilog: 1 circuit, main circuit main
module main (
  input  a,
  input  b,
  input  c,
  input  d,
  output s
);

  wire and_1_out, and_2_out, and_3_out, and_4_out, and_5_out, and_6_out, and_7_out, and_8_out, not_1_out,
       not_2_out, not_3_out, not_4_out, not_5_out, not_6_out, not_7_out, not_8_out, not_9_out, not_10_out,
       not_11_out, not_12_out, not_13_out, not_14_out, not_15_out, not_16_out;

  not not_1 (not_1_out, a);
  not not_2 (not_2_out, c);
  not not_3 (not_3_out, b);
  not not_4 (not_4_out, a);
  not not_5 (not_5_out, b);
  and and_1 (and_1_out, not_4_out, not_3_out, not_2_out, d);
  not not_6 (not_6_out, d);
  not not_7 (not_7_out, c);
  not not_8 (not_8_out, a);
  not not_9 (not_9_out, d);
  and and_2 (and_2_out, not_1_out, not_5_out, c, not_6_out);
  and and_3 (and_3_out, not_8_out, b, not_7_out, not_9_out);
  not not_10 (not_10_out, a);
  and and_4 (and_4_out, not_10_out, b, c, d);
  or or_1 (s, and_1_out, and_2_out, and_3_out, and_4_out, and_5_out, and_7_out, and_6_out, and_8_out);
  not not_11 (not_11_out, b);
  not not_12 (not_12_out, b);
  not not_13 (not_13_out, d);
  not not_14 (not_14_out, c);
  and and_5 (and_5_out, a, not_12_out, not_14_out, not_13_out);
  not not_15 (not_15_out, c);
  and and_6 (and_6_out, a, b, not_15_out, d);
  and and_7 (and_7_out, a, not_11_out, c, d);
  not not_16 (not_16_out, d);
  and and_8 (and_8_out, a, b, c, not_16_out);
endmodule
