// Logisim project prova01-d.circ as structural Verilog: 1 circuit, main circuit main
module main (
  input  a,
  input  b,
  input  c,
  input  d,
  output s
);

  wire not_1_out, not_2_out, not_3_out, not_4_out, not_5_out, not_6_out, not_7_out, not_8_out, not_9_out,
       not_10_out, not_11_out, not_12_out, not_13_out, not_14_out, not_15_out, or_1_out, or_2_out, or_3_out,
       or_4_out, or_5_out, or_6_out, or_7_out, or_8_out;

  or or_1 (or_1_out, a, b, c, d);
  not not_1 (not_1_out, c);
  not not_2 (not_2_out, d);
  or or_2 (or_2_out, a, b, not_1_out, not_2_out);
  not not_3 (not_3_out, b);
  not not_4 (not_4_out, d);
  not not_5 (not_5_out, b);
  or or_3 (or_3_out, a, not_3_out, c, not_4_out);
  not not_6 (not_6_out, c);
  not not_7 (not_7_out, a);
  not not_8 (not_8_out, d);
  or or_4 (or_4_out, not_7_out, b, c, not_8_out);
  or or_5 (or_5_out, a, not_5_out, not_6_out, d);
  and and_1 (s, or_1_out, or_2_out, or_3_out, or_5_out, or_4_out, or_6_out, or_7_out, or_8_out);
  not not_9 (not_9_out, a);
  not not_10 (not_10_out, c);
  or or_6 (or_6_out, not_9_out, b, not_10_out, d);
  not not_11 (not_11_out, b);
  not not_12 (not_12_out, b);
  not not_13 (not_13_out, a);
  not not_14 (not_14_out, a);
  or or_7 (or_7_out, not_14_out, not_11_out, c, d);
  not not_15 (not_15_out, c);
  or or_8 (or_8_out, not_13_out, not_12_out, not_15_out, d);
endmodule
