// Logisim project prova01-f.circ as structural Verilog: 1 circuit, main circuit main
module main (
  input  a,
  input  b,
  input  c,
  input  d,
  output s
);

  wire and_1_out, and_2_out, and_3_out, and_4_out, and_5_out, and_6_out, and_7_out, and_8_out, not_1_out,
       not_2_out, not_3_out, not_4_out, xor_1_out, xor_2_out, xor_3_out, xor_4_out;

  not not_1 (not_1_out, a);
  not not_2 (not_2_out, b);
  and and_1 (and_1_out, not_1_out, not_2_out);
  xor xor_1 (xor_1_out, c, d);
  and and_2 (and_2_out, and_1_out, xor_1_out);
  and and_3 (and_3_out, b, d);
  and and_4 (and_4_out, and_3_out, xor_2_out);
  not not_3 (not_3_out, c);
  xor xor_2 (xor_2_out, a, c);
  or or_1 (s, and_2_out, and_4_out, and_6_out, and_8_out);
  not not_4 (not_4_out, d);
  and and_5 (and_5_out, not_3_out, not_4_out);
  xor xor_3 (xor_3_out, a, b);
  and and_6 (and_6_out, and_5_out, xor_3_out);
  and and_7 (and_7_out, a, c);
  and and_8 (and_8_out, and_7_out, xor_4_out);
  xor xor_4 (xor_4_out, b, d);
endmodule
