// Logisim project prova01-g.circ as structural Verilog: 1 circuit, main circuit main
module main (
  input  a,
  input  b,
  input  c,
  input  d,
  output s
);

  wire and_1_out, and_2_out, and_3_out, and_4_out, and_5_out, and_6_out, and_7_out, and_8_out, and_9_out,
       not_1_out, not_2_out, not_3_out, not_4_out, not_5_out, not_6_out, not_7_out, not_8_out, not_9_out;

  not not_1 (not_1_out, a);
  and and_1 (and_1_out, not_1_out, c, d);
  not not_2 (not_2_out, b);
  and and_2 (and_2_out, not_2_out, c, d);
  not not_3 (not_3_out, a);
  not not_4 (not_4_out, c);
  and and_3 (and_3_out, b, not_4_out, d);
  not not_5 (not_5_out, b);
  and and_4 (and_4_out, not_3_out, b, c);
  and and_5 (and_5_out, a, not_5_out, d);
  or or_1 (s, and_1_out, and_2_out, and_3_out, and_4_out, and_5_out, and_6_out, and_7_out, and_8_out, and_9_out);
  not not_6 (not_6_out, c);
  and and_6 (and_6_out, a, not_6_out, d);
  not not_7 (not_7_out, b);
  and and_7 (and_7_out, a, not_7_out, c);
  not not_8 (not_8_out, d);
  not not_9 (not_9_out, c);
  and and_8 (and_8_out, a, b, not_9_out);
  and and_9 (and_9_out, a, c, not_8_out);
endmodule
