// Logisim project prova01-i.circ as structural Verilog: 1 circuit, main circuit main
module main (
  input  a,
  input  b,
  input  c,
  input  d,
  output s
);

  wire and_1_out, and_2_out, and_3_out, and_4_out, xor_1_out, xor_2_out, xor_3_out, xor_4_out;

  xor xor_1 (xor_1_out, a, c);
  and and_1 (and_1_out, d, xor_1_out);
  and and_2 (and_2_out, d, xor_2_out);
  xor xor_2 (xor_2_out, b, c);
  or or_1 (s, and_1_out, and_2_out, and_3_out, and_4_out);
  xor xor_3 (xor_3_out, a, b);
  and and_3 (and_3_out, c, xor_3_out);
  and and_4 (and_4_out, a, xor_4_out);
  xor xor_4 (xor_4_out, b, d);
endmodule
