// Logisim project prova01-j.circ as structural Verilog: 1 circuit, main circuit main
module main (
  input  a,
  input  b,
  input  c,
  input  d,
  output s,
  output s_2
);

  and and_1 (s, a, b, c, d);
endmodule
