// Logisim project Prova-1.circ as structural Verilog: 8 circuits, main circuit b
module b (
  input  a,
  input  b,
  input  c,
  input  d,
  output saida
);

  wire and_1_out, and_2_out, and_3_out, and_4_out, and_5_out, and_6_out, and_7_out, and_8_out, not_1_out,
       not_2_out, not_3_out, not_4_out, not_5_out, not_6_out, not_7_out, not_8_out, not_9_out, not_10_out,
       not_11_out, not_12_out, not_13_out, not_14_out, not_15_out, not_16_out;

  not not_1 (not_1_out, a);
  not not_2 (not_2_out, b);
  not not_3 (not_3_out, c);
  not not_4 (not_4_out, a);
  not not_5 (not_5_out, b);
  not not_6 (not_6_out, d);
  not not_7 (not_7_out, a);
  not not_8 (not_8_out, c);
  not not_9 (not_9_out, d);
  not not_10 (not_10_out, a);
  not not_11 (not_11_out, b);
  not not_12 (not_12_out, c);
  not not_13 (not_13_out, d);
  not not_14 (not_14_out, b);
  not not_15 (not_15_out, c);
  not not_16 (not_16_out, d);
  and and_1 (and_1_out, not_1_out, not_2_out, not_3_out, d);
  and and_2 (and_2_out, not_4_out, not_5_out, c, not_6_out);
  and and_3 (and_3_out, not_7_out, b, not_8_out, not_9_out);
  and and_4 (and_4_out, not_10_out, b, c, d);
  and and_5 (and_5_out, a, not_11_out, not_12_out, not_13_out);
  and and_6 (and_6_out, a, not_14_out, c, d);
  and and_7 (and_7_out, a, b, not_15_out, d);
  and and_8 (and_8_out, a, b, c, not_16_out);
  or or_1 (saida, and_1_out, and_2_out, and_3_out, and_4_out, and_5_out, and_6_out, and_7_out, and_8_out);

  // Notes on the sheet:
  //   t1,t2,t3
  //   t5,t6,t7
  //   t9,t10,t11
  //   t13
  //   t15,t16,t17
  //   t19
  //   t21
  //   t23
  //   t14
  //   Isabella Gonçales - 420120
  //   t4
  //   t8
  //   t12
  //   t18
  //   t20
  //   t22
  //   t24
endmodule

module c (
  input  a,
  input  b,
  input  c,
  input  d,
  output saida
);

  wire and_1_out, and_2_out, and_3_out, and_4_out, and_5_out, and_6_out, and_7_out, and_8_out, and_9_out,
       and_10_out, not_1_out, not_2_out, not_3_out, not_4_out, not_5_out, not_6_out, not_7_out, not_8_out,
       not_9_out, not_10_out, not_11_out, not_12_out, not_13_out, t4_t5_out, t7_t8_out, t10_out;

  not not_1 (not_1_out, a);
  not not_2 (not_2_out, b);
  not t4_t5 (t4_t5_out, a);
  not not_3 (not_3_out, c);
  not t7_t8 (t7_t8_out, a);
  not not_4 (not_4_out, d);
  not t10 (t10_out, a);
  not not_5 (not_5_out, b);
  not not_6 (not_6_out, c);
  not not_7 (not_7_out, b);
  not not_8 (not_8_out, d);
  not not_9 (not_9_out, b);
  not not_10 (not_10_out, c);
  not not_11 (not_11_out, d);
  not not_12 (not_12_out, c);
  not not_13 (not_13_out, d);
  and and_1 (and_1_out, not_1_out, not_2_out, c, d);
  and and_2 (and_2_out, t4_t5_out, b, not_3_out, d);
  and and_3 (and_3_out, t7_t8_out, b, c, not_4_out);
  and and_4 (and_4_out, t10_out, b, c, d);
  and and_5 (and_5_out, a, not_5_out, not_6_out, d);
  and and_6 (and_6_out, a, not_7_out, c, not_8_out);
  and and_7 (and_7_out, a, not_9_out, c, d);
  and and_8 (and_8_out, a, b, not_10_out, not_11_out);
  and and_9 (and_9_out, a, b, not_12_out, d);
  and and_10 (and_10_out, a, b, c, not_13_out);
  or or_1 (saida, and_1_out, and_2_out, and_3_out, and_4_out, and_5_out, and_6_out, and_7_out, and_8_out, and_9_out, and_10_out);

  // Notes on the sheet:
  //   t1,t2
  //   t12,t13
  //   t15,t16
  //   t18
  //   t20,t21
  //   t23
  //   t25
  //   Isabella Gonçales - 420120
  //   t11
  //   t14
  //   t17
  //   t19
  //   t3
  //   t6
  //   t9
  //   t22
  //   T24
  //   t26
endmodule

module d (
  input  a,
  input  b,
  input  c,
  input  d,
  output saida
);

  wire not_1_out, not_2_out, not_3_out, not_4_out, not_5_out, not_6_out, not_7_out, not_8_out, not_9_out,
       not_10_out, not_11_out, not_12_out, not_13_out, not_14_out, or_1_out, or_2_out, or_3_out, or_4_out,
       or_5_out, or_6_out, or_7_out, or_8_out, t11_t12_out, t14_t5_out;

  not not_1 (not_1_out, c);
  not not_2 (not_2_out, d);
  not not_3 (not_3_out, b);
  not not_4 (not_4_out, d);
  not not_5 (not_5_out, b);
  not not_6 (not_6_out, c);
  not t11_t12 (t11_t12_out, a);
  not not_7 (not_7_out, d);
  not t14_t5 (t14_t5_out, a);
  not not_8 (not_8_out, c);
  not not_9 (not_9_out, a);
  not not_10 (not_10_out, b);
  not not_11 (not_11_out, a);
  not not_12 (not_12_out, b);
  not not_13 (not_13_out, c);
  not not_14 (not_14_out, d);
  or or_1 (or_1_out, a, b, c, d);
  or or_2 (or_2_out, a, b, not_1_out, not_2_out);
  or or_3 (or_3_out, a, not_3_out, c, not_4_out);
  or or_4 (or_4_out, a, not_5_out, not_6_out, d);
  or or_5 (or_5_out, t11_t12_out, b, c, not_7_out);
  or or_6 (or_6_out, t14_t5_out, b, not_8_out, d);
  or or_7 (or_7_out, not_9_out, not_10_out, c, d);
  or or_8 (or_8_out, not_11_out, not_12_out, not_13_out, not_14_out);
  and and_1 (saida, or_1_out, or_2_out, or_3_out, or_4_out, or_5_out, or_6_out, or_7_out, or_8_out);

  // Notes on the sheet:
  //   t2,t3
  //   t5,t6
  //   t8,t9
  //   t17,t18
  //   t20,t21,t22,t23
  //   t4
  //   t7
  //   t10
  //   t13
  //   t16
  //   t19
  //   t24
  //   Isabella Gonçales -420120
  //   t1
endmodule

module e (
  input  a,
  input  b,
  input  c,
  input  d,
  output saida
);

  wire and_1_out, and_2_out, and_3_out, and_4_out, and_5_out, and_6_out, and_7_out, and_8_out, not_1_out,
       not_2_out, not_3_out, not_4_out, not_5_out, not_6_out, not_7_out, not_8_out, not_9_out, not_10_out,
       not_11_out, not_12_out, not_13_out, not_14_out, not_15_out, not_16_out;

  not not_1 (not_1_out, a);
  not not_2 (not_2_out, b);
  not not_3 (not_3_out, c);
  not not_4 (not_4_out, a);
  not not_5 (not_5_out, b);
  not not_6 (not_6_out, d);
  not not_7 (not_7_out, a);
  not not_8 (not_8_out, c);
  not not_9 (not_9_out, d);
  not not_10 (not_10_out, a);
  not not_11 (not_11_out, b);
  not not_12 (not_12_out, c);
  not not_13 (not_13_out, d);
  not not_14 (not_14_out, b);
  not not_15 (not_15_out, c);
  not not_16 (not_16_out, d);
  and and_1 (and_1_out, not_1_out, not_2_out, not_3_out, d);
  and and_2 (and_2_out, not_4_out, not_5_out, c, not_6_out);
  and and_3 (and_3_out, not_7_out, b, not_8_out, not_9_out);
  and and_4 (and_4_out, not_10_out, b, c, d);
  and and_5 (and_5_out, a, not_11_out, not_12_out, not_13_out);
  and and_6 (and_6_out, a, not_14_out, c, d);
  and and_7 (and_7_out, a, b, not_15_out, d);
  and and_8 (and_8_out, a, b, c, not_16_out);
  or or_1 (saida, and_1_out, and_2_out, and_3_out, and_4_out, and_5_out, and_6_out, and_7_out, and_8_out);

  // Notes on the sheet:
  //   t1,t2,t3
  //   t5,t6,t7
  //   t9,y10,t11
  //   t13
  //   t15,t16,t17
  //   t19
  //   t21
  //   t23
  //   t14
  //   Isabella Gonçales - 420120
  //   t4
  //   t8
  //   t12
  //   t18
  //   t20
  //   t22
  //   t24
endmodule

module f (
  input  a,
  input  b,
  input  c,
  input  d,
  output saida
);

  wire and_1_out, and_2_out, and_3_out, and_4_out, and_5_out, and_6_out, and_7_out, and_8_out, not_1_out,
       not_2_out, not_3_out, not_4_out, xor_1_out, xor_2_out, xor_3_out, xor_4_out;

  not not_1 (not_1_out, b);
  not not_2 (not_2_out, c);
  not not_3 (not_3_out, a);
  not not_4 (not_4_out, d);
  and and_1 (and_1_out, not_1_out, not_2_out);
  xor xor_1 (xor_1_out, a, b);
  and and_2 (and_2_out, not_3_out, not_4_out);
  xor xor_2 (xor_2_out, b, c);
  and and_3 (and_3_out, c, d);
  xor xor_3 (xor_3_out, a, b);
  and and_4 (and_4_out, a, b);
  xor xor_4 (xor_4_out, c, d);
  and and_5 (and_5_out, and_1_out, xor_1_out);
  and and_6 (and_6_out, and_2_out, xor_2_out);
  and and_7 (and_7_out, and_3_out, xor_3_out);
  and and_8 (and_8_out, and_4_out, xor_4_out);
  or or_1 (saida, and_5_out, and_6_out, and_7_out, and_8_out);

  // Notes on the sheet:
  //   t1,t2
  //   t6,t7
  //   t3
  //   t4
  //   t8
  //   t9
  //   t11
  //   t12
  //   t14
  //   t15
  //   Isabella Gonçales - 420120
  //   t5
  //   t10
  //   t13
  //   t16
endmodule

module g (
  input  a,
  input  b,
  input  c,
  input  d,
  output saida
);

  wire and_1_out, and_2_out, and_3_out, and_4_out, and_5_out, and_6_out, not_1_out, not_2_out, not_3_out,
       not_4_out, not_5_out, not_6_out;

  not not_1 (not_1_out, b);
  not not_2 (not_2_out, c);
  not not_3 (not_3_out, a);
  not not_4 (not_4_out, b);
  not not_5 (not_5_out, b);
  not not_6 (not_6_out, d);
  and and_1 (and_1_out, not_1_out, c, d);
  and and_2 (and_2_out, b, not_2_out, d);
  and and_3 (and_3_out, not_3_out, b, c);
  and and_4 (and_4_out, a, not_4_out, d);
  and and_5 (and_5_out, a, not_5_out, c);
  and and_6 (and_6_out, a, b, not_6_out);
  or or_1 (saida, and_1_out, and_2_out, and_3_out, and_4_out, and_5_out, and_6_out);

  // Notes on the sheet:
  //   t1
  //   t3
  //   t5
  //   t7
  //   t9
  //   t11
  //   t2
  //   t4
  //   t6
  //   t8
  //   t10
  //   t12
  //   Isabella Gonçales - 420120
endmodule

module i (
  input  a,
  input  b,
  input  c,
  input  d,
  output saida
);

  wire and_1_out, and_2_out, and_3_out, and_4_out, and_5_out, not_1_out, not_2_out, or_1_out, xor_1_out,
       xor_2_out;

  xor xor_1 (xor_1_out, a, d);
  not not_1 (not_1_out, c);
  not not_2 (not_2_out, d);
  and and_1 (and_1_out, xor_1_out, c);
  xor xor_2 (xor_2_out, a, b);
  and and_2 (and_2_out, xor_2_out, d);
  and and_3 (and_3_out, b, not_1_out);
  and and_4 (and_4_out, c, not_2_out);
  or or_1 (or_1_out, and_3_out, and_4_out);
  and and_5 (and_5_out, a, or_1_out);
  or or_2 (saida, and_1_out, and_2_out, and_5_out);

  // Notes on the sheet:
  //   t7
  //   t1
  //   t5
  //   Isabella Gonçales - 420120
  //   t3
  //   t6
  //   t8
  //   t2
  //   t4
  //   t9
  //   t10
endmodule

module j (
  input  a,
  input  b,
  input  c,
  input  d,
  output saida
);

  and and_1 (saida, a, b, c, d);

  // Notes on the sheet:
  //   Isabella Gonçales - 420120
endmodule
