// Logisim project circ.circ as structural Verilog: 8 circuits, main circuit letrab
module letrab (
  input  a,
  input  b,
  input  c,
  input  d,
  output s
);

  wire and_1_out, and_2_out, and_3_out, and_4_out, and_5_out, and_6_out, and_7_out, and_8_out, not_1_out,
       not_2_out, not_3_out, not_4_out, not_5_out, not_6_out, not_7_out, not_8_out, not_9_out, not_10_out,
       not_11_out, not_12_out, not_13_out, not_14_out, not_15_out, not_16_out;

  not not_1 (not_1_out, a);
  not not_2 (not_2_out, b);
  not not_3 (not_3_out, c);
  not not_4 (not_4_out, a);
  not not_5 (not_5_out, b);
  not not_6 (not_6_out, d);
  not not_7 (not_7_out, a);
  not not_8 (not_8_out, c);
  not not_9 (not_9_out, d);
  not not_10 (not_10_out, a);
  not not_11 (not_11_out, b);
  not not_12 (not_12_out, c);
  not not_13 (not_13_out, d);
  not not_14 (not_14_out, b);
  not not_15 (not_15_out, c);
  not not_16 (not_16_out, d);
  and and_1 (and_1_out, not_1_out, d, not_2_out, not_3_out);
  and and_2 (and_2_out, not_4_out, c, not_5_out, not_6_out);
  and and_3 (and_3_out, not_7_out, b, not_8_out, not_9_out);
  and and_4 (and_4_out, not_10_out, b, c, d);
  and and_5 (and_5_out, not_11_out, a, not_12_out, not_13_out);
  and and_6 (and_6_out, not_14_out, a, c, d);
  and and_7 (and_7_out, not_15_out, a, b, d);
  and and_8 (and_8_out, not_16_out, a, b, c);
  or or_1 (s, and_1_out, and_2_out, and_3_out, and_4_out, and_5_out, and_6_out, and_7_out, and_8_out);

  // Notes on the sheet:
  //   Prova02 - letrab
  //   s1
  //   s2
  //   s3
  //   s4
  //   s5
  //   s6
  //   s7
  //   s8
endmodule

module letrac (
  input  a,
  input  b,
  input  c,
  input  d,
  output s
);

  wire and_1_out, and_2_out, and_3_out, and_4_out, and_5_out, and_6_out, and_7_out, and_8_out, and_9_out,
       and_10_out, not_1_out, not_2_out, not_3_out, not_4_out, not_5_out, not_6_out, not_7_out, not_8_out,
       not_9_out, not_10_out, not_11_out, not_12_out, not_13_out, not_14_out, not_15_out, not_16_out;

  not not_1 (not_1_out, a);
  not not_2 (not_2_out, b);
  not not_3 (not_3_out, a);
  not not_4 (not_4_out, c);
  not not_5 (not_5_out, a);
  not not_6 (not_6_out, d);
  not not_7 (not_7_out, a);
  not not_8 (not_8_out, b);
  not not_9 (not_9_out, c);
  not not_10 (not_10_out, b);
  not not_11 (not_11_out, d);
  not not_12 (not_12_out, b);
  not not_13 (not_13_out, c);
  not not_14 (not_14_out, d);
  not not_15 (not_15_out, c);
  not not_16 (not_16_out, d);
  and and_1 (and_1_out, not_1_out, not_2_out, c, d);
  and and_2 (and_2_out, not_3_out, not_4_out, b, d);
  and and_3 (and_3_out, not_5_out, not_6_out, b, c);
  and and_4 (and_4_out, not_7_out, b, c, d);
  and and_5 (and_5_out, not_8_out, not_9_out, a, d);
  and and_6 (and_6_out, not_10_out, not_11_out, a, c);
  and and_7 (and_7_out, not_12_out, a, c, d);
  and and_8 (and_8_out, not_13_out, not_14_out, a, b);
  and and_9 (and_9_out, not_15_out, a, b, d);
  and and_10 (and_10_out, not_16_out, a, b, c);
  or or_1 (s, and_1_out, and_2_out, and_3_out, and_4_out, and_5_out, and_6_out, and_7_out, and_8_out, and_9_out, and_10_out);

  // Notes on the sheet:
  //   Prova01 - letrac
  //   s1
  //   s2
  //   s3
  //   s4
  //   s5
  //   s6
  //   s7
  //   s8
  //   s9
  //   s10
endmodule

module letrad (
  input  a,
  input  b,
  input  c,
  input  d,
  output s
);

  wire not_1_out, not_2_out, not_3_out, not_4_out, not_5_out, not_6_out, not_7_out, not_8_out, not_9_out,
       not_10_out, not_11_out, not_12_out, not_13_out, not_14_out, not_15_out, not_16_out, or_1_out,
       or_2_out, or_3_out, or_4_out, or_5_out, or_6_out, or_7_out, or_8_out;

  not not_1 (not_1_out, c);
  not not_2 (not_2_out, d);
  not not_3 (not_3_out, b);
  not not_4 (not_4_out, d);
  not not_5 (not_5_out, b);
  not not_6 (not_6_out, c);
  not not_7 (not_7_out, a);
  not not_8 (not_8_out, d);
  not not_9 (not_9_out, a);
  not not_10 (not_10_out, c);
  not not_11 (not_11_out, a);
  not not_12 (not_12_out, b);
  not not_13 (not_13_out, a);
  not not_14 (not_14_out, c);
  or or_1 (or_1_out, a, b, c, d);
  or or_2 (or_2_out, not_1_out, not_2_out, a, b);
  or or_3 (or_3_out, not_3_out, not_4_out, a, c);
  or or_4 (or_4_out, not_5_out, not_6_out, a, d);
  or or_5 (or_5_out, not_7_out, not_8_out, b, c);
  or or_6 (or_6_out, not_9_out, not_10_out, b, d);
  or or_7 (or_7_out, not_11_out, not_12_out, c, d);
  not not_15 (not_15_out, b);
  not not_16 (not_16_out, d);
  or or_8 (or_8_out, not_13_out, not_15_out, not_14_out, not_16_out);
  and and_1 (s, or_1_out, or_2_out, or_3_out, or_4_out, or_5_out, or_6_out, or_7_out, or_8_out);

  // Notes on the sheet:
  //   Prova01 - letrad
  //   s2
  //   s6
  //   s7
  //   s1
  //   s3
  //   s4
  //   s5
  //   s8
endmodule

module letrae (
  input  a,
  input  b,
  input  c,
  input  d,
  output s
);

  wire and_1_out, and_2_out, and_3_out, and_4_out, and_5_out, and_6_out, and_7_out, and_8_out, not_1_out,
       not_2_out, not_3_out, not_4_out, not_5_out, not_6_out, not_7_out, not_8_out, not_9_out, not_10_out,
       not_11_out, not_12_out, not_13_out, not_14_out, not_15_out, not_16_out;

  not not_1 (not_1_out, a);
  not not_2 (not_2_out, b);
  not not_3 (not_3_out, c);
  not not_4 (not_4_out, a);
  not not_5 (not_5_out, b);
  not not_6 (not_6_out, d);
  not not_7 (not_7_out, a);
  not not_8 (not_8_out, c);
  not not_9 (not_9_out, d);
  not not_10 (not_10_out, b);
  not not_11 (not_11_out, c);
  not not_12 (not_12_out, d);
  not not_13 (not_13_out, b);
  not not_14 (not_14_out, c);
  not not_15 (not_15_out, a);
  not not_16 (not_16_out, d);
  and and_1 (and_1_out, not_1_out, d, not_2_out, not_3_out);
  and and_2 (and_2_out, not_4_out, c, not_5_out, not_6_out);
  and and_3 (and_3_out, not_7_out, b, not_8_out, not_9_out);
  and and_4 (and_4_out, not_10_out, a, not_11_out, not_12_out);
  and and_5 (and_5_out, not_13_out, a, c, d);
  and and_6 (and_6_out, not_14_out, a, b, d);
  and and_7 (and_7_out, not_15_out, b, c, d);
  and and_8 (and_8_out, not_16_out, a, b, c);
  or or_1 (s, and_1_out, and_2_out, and_3_out, and_4_out, and_5_out, and_6_out, and_7_out, and_8_out);

  // Notes on the sheet:
  //   Prova01 - letrae
  //   s1
  //   s2
  //   s3
  //   s4
  //   s5
  //   s6
  //   s7
  //   s8
endmodule

module letraf (
  input  a,
  input  b,
  input  c,
  input  d,
  output s
);

  wire and_1_out, and_2_out, and_3_out, and_4_out, not_1_out, not_2_out, not_3_out, not_4_out, xor_1_out,
       xor_2_out, xor_3_out, xor_4_out;

  xor xor_1 (xor_1_out, c, d);
  xor xor_2 (xor_2_out, a, c);
  xor xor_3 (xor_3_out, a, b);
  xor xor_4 (xor_4_out, b, d);
  not not_1 (not_1_out, a);
  not not_2 (not_2_out, b);
  not not_3 (not_3_out, c);
  not not_4 (not_4_out, d);
  and and_1 (and_1_out, xor_1_out, not_1_out, not_2_out);
  and and_2 (and_2_out, xor_2_out, b, d);
  and and_3 (and_3_out, xor_3_out, not_3_out, not_4_out);
  and and_4 (and_4_out, xor_4_out, c, a);
  or or_1 (s, and_1_out, and_2_out, and_3_out, and_4_out);

  // Notes on the sheet:
  //   Prova01 - letraf
  //   s1
  //   s2
  //   s3
  //   s4
  //   s5
  //   s6
  //   s7
  //   s8
endmodule

module letrag (
  input  a,
  input  b,
  input  c,
  input  d,
  output s
);

  wire and_1_out, and_2_out, and_3_out, and_4_out, and_5_out, and_6_out, and_7_out, and_8_out, and_9_out,
       not_1_out, not_2_out, not_3_out, not_4_out, not_5_out, not_6_out, not_7_out, not_8_out, not_9_out;

  not not_1 (not_1_out, a);
  not not_2 (not_2_out, b);
  not not_3 (not_3_out, c);
  not not_4 (not_4_out, a);
  not not_5 (not_5_out, b);
  not not_6 (not_6_out, c);
  not not_7 (not_7_out, b);
  not not_8 (not_8_out, c);
  not not_9 (not_9_out, d);
  and and_1 (and_1_out, not_1_out, c, d);
  and and_2 (and_2_out, not_2_out, c, d);
  and and_3 (and_3_out, not_3_out, b, d);
  and and_4 (and_4_out, not_4_out, b, c);
  and and_5 (and_5_out, not_5_out, a, d);
  and and_6 (and_6_out, not_6_out, a, d);
  and and_7 (and_7_out, not_7_out, a, c);
  and and_8 (and_8_out, not_8_out, a, b);
  and and_9 (and_9_out, not_9_out, a, b);
  or or_1 (s, and_1_out, and_2_out, and_3_out, and_4_out, and_5_out, and_6_out, and_7_out, and_8_out, and_9_out);

  // Notes on the sheet:
  //   Prova01 - letrag
  //   s1
  //   s2
  //   s4
  //   s5
  //   s6
  //   s7
  //   s8
  //   s3
  //   s9
endmodule

module letrai (
  input  a,
  input  b,
  input  c,
  input  d,
  output s
);

  wire and_1_out, and_2_out, and_3_out, and_4_out, xor_1_out, xor_2_out, xor_3_out, xor_4_out;

  xor xor_1 (xor_1_out, a, c);
  xor xor_2 (xor_2_out, b, c);
  xor xor_3 (xor_3_out, a, b);
  xor xor_4 (xor_4_out, b, d);
  and and_1 (and_1_out, xor_1_out, d);
  and and_2 (and_2_out, xor_2_out, d);
  and and_3 (and_3_out, xor_3_out, c);
  and and_4 (and_4_out, xor_4_out, a);
  or or_1 (s, and_1_out, and_2_out, and_3_out, and_4_out);

  // Notes on the sheet:
  //   Prova01 - letrai
  //   s1
  //   s2
  //   s3
  //   s4
  //   s5
  //   s6
  //   s7
  //   s8
endmodule

module letraj (
  input  a,
  input  b,
  input  c,
  input  d,
  output s
);

  and and_1 (s, a, b, c, d);

  // Notes on the sheet:
  //   Prova 01 - letraj
endmodule
