// Logisim project exercicio_01.circ as structural Verilog: 1 circuit, main circuit main
module main (
  input  p,
  input  q,
  output s
);

  wire nand_1_out, nand_2_out;

  nand nand_1 (nand_1_out, p, p);
  nand nand_2 (nand_2_out, q, q);
  nand nand_3 (s, nand_1_out, nand_2_out);
endmodule
