// Logisim project exercicio_02.circ as structural Verilog: 1 circuit, main circuit main
module main (
  input  p,
  input  q,
  output s
);

  wire nor_1_out, nor_2_out;

  nor nor_1 (nor_1_out, p, p);
  nor nor_2 (nor_2_out, q, q);
  nor nor_3 (s, nor_1_out, nor_2_out);
endmodule
