// Logisim project Nand.circ as structural Verilog: 1 circuit, main circuit main
module main (
  input  a,
  input  b,
  input  c,
  output s
);

  wire undriven, undriven_2;

  nand nand_1 (s, undriven, a, b, c, undriven_2);
  // AND_Gate and_1 has open pins: in0=undriven, in1=a, in2=b, in3=c, in4=undriven_2, out=open
endmodule
