// Logisim project Nor.circ as structural Verilog: 1 circuit, main circuit main
module main (
  input  in_1,
  input  in_2,
  input  in_3,
  output out_4
);

  nor nor_1 (out_4, in_1, in_2, in_3);
endmodule
