// Logisim project Exemplo 01.circ as structural Verilog: 2 circuits, main circuit Meia Soma
module Meia_Soma (
  input  a,
  input  b,
  output s0,
  output s1
);

  wire not_1_out, or_1_out;

  or or_1 (or_1_out, a, b);
  and and_1 (s1, a, b);
  not not_1 (not_1_out, s1);
  and and_2 (s0, or_1_out, not_1_out);

  // Notes on the sheet:
  //   Nome: Bruno Rafael Nicolletti - Matrícula: 380752
endmodule

module main (
  input  a,
  input  b,
  output s0,
  output s1
);

  Meia_Soma meia_soma_1 (.a(a), .b(b), .s0(s0), .s1(s1));

  // Notes on the sheet:
  //   Nome: Bruno Rafael Nicolletti - Matrícula: 380752
endmodule
