// Logisim project Exemplo 02.circ as structural Verilog: 2 circuits, main circuit Meia Soma Com NAND
module Meia_Soma_Com_NAND (
  input  a,
  input  b,
  output s0,
  output s1
);

  wire nand_1_out, nand_2_out, nand_3_out, nand_5_out, nand_6_out, nand_7_out;

  nand nand_1 (nand_1_out, a, b);
  nand nand_2 (nand_2_out, a, a);
  nand nand_3 (nand_3_out, b, b);
  nand nand_4 (s1, nand_1_out, nand_1_out);
  nand nand_5 (nand_5_out, nand_2_out, nand_3_out);
  nand nand_6 (nand_6_out, s1, s1);
  nand nand_7 (nand_7_out, nand_5_out, nand_6_out);
  nand nand_8 (s0, nand_7_out, nand_7_out);

  // Notes on the sheet:
  //   Nome: Bruno Rafael Nicolletti - Matrícula: 380752
endmodule

module main (
  input  a,
  input  b,
  output s0,
  output s1
);

  Meia_Soma_Com_NAND meia_soma_com_nand_1 (.a(a), .b(b), .s0(s0), .s1(s1));

  // Notes on the sheet:
  //   Nome: Bruno Rafael Nicolletti - Matrícula: 380752
endmodule
