// Logisim project Exemplo 03.circ as structural Verilog: 2 circuits, main circuit main
module main (
  input  a,
  input  b,
  output s0,
  output s1
);

  \Meia_Diferença_com_NAND  \meia_diferença_com_nand_1  (.a(a), .b(b), .s0(s0), .s1(s1));

  // Notes on the sheet:
  //   Nome: Bruno Rafael Nicolletti - Matrícula: 380752
endmodule

module \Meia_Diferença_com_NAND  (
  input  a,
  input  b,
  output s0,
  output s1
);

  wire nand_1_out, nand_2_out, nand_3_out, nand_4_out, nand_5_out;

  nand nand_1 (nand_1_out, a, b);
  nand nand_2 (nand_2_out, a, a);
  nand nand_3 (nand_3_out, a, nand_1_out);
  nand nand_4 (nand_4_out, nand_1_out, b);
  nand nand_5 (nand_5_out, b, nand_2_out);
  nand nand_6 (s0, nand_3_out, nand_4_out);
  nand nand_7 (s1, nand_5_out, nand_5_out);

  // Notes on the sheet:
  //   Nome: Bruno Rafael Nicolletti - Matrícula: 380752
endmodule
