// Logisim project ex_02.circ as structural Verilog: 1 circuit, main circuit main
module main (
  input  a,
  input  b,
  output s0,
  output s1
);

  wire nand_1_out, nand_2_out, nand_4_out, nand_5_out;

  nand nand_1 (nand_1_out, a, b);
  nand nand_2 (nand_2_out, a, b);
  nand nand_3 (s0, nand_1_out, nand_1_out);
  nand nand_4 (nand_4_out, a, nand_2_out);
  nand nand_5 (nand_5_out, nand_2_out, b);
  and and_1 (s1, nand_4_out, nand_4_out, nand_5_out);
endmodule
