// Logisim project ex_03.circ as structural Verilog: 1 circuit, main circuit main
module main (
  input  b,
  input  a,
  output s0,
  output s1
);

  wire nand_1_out, nand_2_out, nand_3_out, nand_4_out, nand_5_out;

  nand nand_1 (nand_1_out, b, b, a);
  nand nand_2 (nand_2_out, b, a);
  nand nand_3 (nand_3_out, b, nand_1_out);
  nand nand_4 (nand_4_out, nand_1_out, nand_1_out, a);
  nand nand_5 (nand_5_out, b, nand_2_out);
  nand nand_6 (s0, nand_3_out, nand_4_out);
  nand nand_7 (s1, nand_5_out, nand_5_out);
endmodule
