// Logisim project guia03_01.circ as structural Verilog: 1 circuit, main circuit main
module main (
  input  A,
  input  B,
  output s0,
  output s1
);

  wire s2_out, s3_out;

  or s2 (s2_out, A, B);
  nand s3 (s3_out, A, B);
  and and_1 (s1, B, A);
  and and_2 (s0, s2_out, s3_out);
endmodule
