// Logisim project guia03_02.circ as structural Verilog: 1 circuit, main circuit main
module main (
  input  A,
  input  B,
  output s1,
  output s1_2
);

  wire s2_out, s3_out, s4_out, s5_out;

  nand s2 (s2_out, A, B);
  nand s3 (s3_out, A, B);
  nand nand_1 (s1, s2_out, s2_out);
  nand s4 (s4_out, A, s3_out);
  nand s5 (s5_out, s3_out, B);
  nand nand_2 (s1_2, s4_out, s5_out);
endmodule
