// Logisim project Guia03Ex1.circ as structural Verilog: 1 circuit, main circuit main
module main (
  input  x,
  input  y,
  output S1,
  output S0
);

  wire not_1_out, OR_out;

  and AND (S1, x, y);
  or OR (OR_out, x, y);
  not not_1 (not_1_out, S1);
  and and_2 (S0, not_1_out, OR_out);

  // Notes on the sheet:
  //   Alvaro Henrique de Araujo Rungue - 395487
endmodule
