// Logisim project Guia03Ex3.circ as structural Verilog: 1 circuit, main circuit main
module main (
  input  a,
  input  b,
  output s1,
  output s0
);

  wire nand_1_out, nand_2_out, nand_3_out, nand_4_out, nand_5_out;

  nand nand_1 (nand_1_out, a, a);
  nand nand_2 (nand_2_out, a, b);
  nand nand_3 (nand_3_out, b, nand_1_out);
  nand nand_4 (nand_4_out, nand_2_out, b);
  nand nand_5 (nand_5_out, a, nand_2_out);
  nand s2 (s0, nand_5_out, nand_4_out);
  nand u_S1 (s1, nand_3_out, nand_3_out);

  // Notes on the sheet:
  //   s6
  //   s3
  //   s7
  //   s5
  //   s4
  //   Alvaro Henrique de Araujo Rungue - 395487
endmodule
