// Logisim project Guia03_01.circ as structural Verilog: 1 circuit, main circuit main
module main (
  input  in_1,
  input  in_2,
  input  a,
  input  b,
  output out_5,
  output out_6,
  output s0,
  output s1
);

  wire NOT_out, OR_out;

  or OR (OR_out, a, b);
  and AND (s1, a, b);
  xor xor_1 (out_5, in_1, in_2);
  and and_2 (out_6, in_1, in_2);
  not NOT (NOT_out, s1);
  and AND2 (s0, OR_out, NOT_out);

  // Notes on the sheet:
  //   Half-Adder para Comparaçao de Resultado
  //   Guia03_02 - Bruno Cézar Andrade Viallet - 396679
endmodule
