// Logisim project Guia03_02.circ as structural Verilog: 1 circuit, main circuit main
module main (
  input  in_1,
  input  in_2,
  input  a,
  input  b,
  output out_5,
  output out_6,
  output s0,
  output s1
);

  wire NAND_2_out, NAND_3_out, NAND_4_out, NAND_out;

  nand NAND (NAND_out, a, a, b);
  nand NAND_2 (NAND_2_out, a, b);
  xor xor_1 (out_5, in_1, in_2);
  and and_1 (out_6, in_1, in_2);
  nand NAND_3 (NAND_3_out, a, NAND_out);
  nand NAND_4 (NAND_4_out, NAND_out, b);
  nand NAND_5 (s1, NAND_2_out, NAND_2_out);
  nand NAND_6 (s0, NAND_3_out, NAND_4_out);

  // Notes on the sheet:
  //   Half-Adder para Comparaçao de Resultado
  //   Guia03_02 - Bruno Cézar Andrade Viallet - 396679
  //   4NANDs = 1 XOR
  //   2NANDs = 1AND
endmodule
