// Logisim project Guia03_03.circ as structural Verilog: 1 circuit, main circuit main
module main (
  input  b,
  input  a,
  input  b_2,
  input  a_2,
  output s1,
  output s0,
  output s0_2,
  output s1_2
);

  wire nand_1_out, nand_2_out, nand_3_out, nand_4_out, nand_5_out, not_1_out;

  not not_1 (not_1_out, a);
  nand nand_1 (nand_1_out, b_2, a_2);
  nand nand_2 (nand_2_out, b_2, a_2);
  xor xor_1 (s1, b, a);
  and and_1 (s0, b, not_1_out);
  nand nand_3 (nand_3_out, b_2, nand_1_out);
  nand nand_4 (nand_4_out, nand_1_out, a_2);
  nand nand_5 (nand_5_out, b_2, nand_2_out);
  nand nand_6 (s0_2, nand_3_out, nand_4_out);
  nand nand_7 (s1_2, nand_5_out, nand_5_out);

  // Notes on the sheet:
  //   Half-Subtractor
  //   Guia03_03 - Bruno Cezar Andrade Viallet - 396679
endmodule
