// Logisim project Guia0302.circ as structural Verilog: 1 circuit, main circuit main
module main (
  input  a,
  input  b,
  output s,
  output c
);

  wire nand_1_out, nand_2_out, nand_3_out, nand_4_out, nand_5_out, nand_6_out, nand_7_out, nand_9_out,
       nand_10_out, nand_11_out;

  not nand_1 (nand_1_out, a);  // NAND_Gate
  not nand_2 (nand_2_out, b);  // NAND_Gate
  nand nand_3 (nand_3_out, nand_1_out, b);
  nand nand_4 (nand_4_out, a, b);
  nand nand_5 (nand_5_out, a, nand_2_out);
  not nand_6 (nand_6_out, nand_3_out);  // NAND_Gate
  not nand_7 (nand_7_out, nand_5_out);  // NAND_Gate
  not nand_8 (c, nand_4_out);  // NAND_Gate
  nand nand_9 (nand_9_out, nand_6_out, nand_7_out);
  nand nand_10 (nand_10_out, nand_6_out, nand_9_out);
  nand nand_11 (nand_11_out, nand_9_out, nand_7_out);
  nand nand_12 (s, nand_10_out, nand_11_out);

  // Notes on the sheet:
  //   Gabriel Benjamim de Carvalho
endmodule
