// Logisim project Guia0303.circ as structural Verilog: 1 circuit, main circuit main
module main (
  input  a,
  input  b,
  output s,
  output c
);

  wire nand_1_out, nand_2_out, nand_3_out, nand_4_out, nand_5_out, nand_6_out, nand_7_out, nand_8_out,
       nand_9_out, nand_11_out, nand_12_out;

  not nand_1 (nand_1_out, a);  // NAND_Gate
  not nand_2 (nand_2_out, b);  // NAND_Gate
  nand nand_3 (nand_3_out, a, nand_2_out);
  not nand_4 (nand_4_out, a);  // NAND_Gate
  nand nand_5 (nand_5_out, nand_1_out, b);
  not nand_6 (nand_6_out, nand_3_out);  // NAND_Gate
  not nand_7 (nand_7_out, nand_5_out);  // NAND_Gate
  nand nand_8 (nand_8_out, nand_4_out, b);
  nand nand_9 (nand_9_out, nand_7_out, nand_6_out);
  not nand_10 (c, nand_8_out);  // NAND_Gate
  nand nand_11 (nand_11_out, nand_7_out, nand_9_out);
  nand nand_12 (nand_12_out, nand_9_out, nand_6_out);
  nand nand_13 (s, nand_11_out, nand_12_out);

  // Notes on the sheet:
  //   Gabriel Benjamim de Carvalho
endmodule
