// Logisim project Guia0305.circ as structural Verilog: 1 circuit, main circuit main
module main (
  input  a,
  input  b,
  output s,
  output c
);

  wire nor_1_out, nor_2_out, nor_3_out, nor_4_out, nor_6_out, nor_7_out;

  not nor_1 (nor_1_out, a);  // NOR_Gate
  not nor_2 (nor_2_out, b);  // NOR_Gate
  nor nor_3 (nor_3_out, nor_1_out, b);
  not nor_4 (nor_4_out, nor_1_out);  // NOR_Gate
  nor nor_5 (c, nor_4_out, nor_2_out);
  nor nor_6 (nor_6_out, a, nor_2_out);
  nor nor_7 (nor_7_out, nor_3_out, nor_6_out);
  not nor_8 (s, nor_7_out);  // NOR_Gate

  // Notes on the sheet:
  //   Gabriel Benjamim de Carvalho
endmodule
