// Logisim project Guia 03_02.circ as structural Verilog: 1 circuit, main circuit main
module main (
  input  a,
  input  b,
  output s1,
  output s0
);

  wire nand_1_out, nand_2_out, nand_4_out, nand_5_out;

  nand nand_1 (nand_1_out, a, b);
  nand nand_2 (nand_2_out, a, b);
  nand nand_3 (s1, nand_1_out, nand_1_out);
  nand nand_4 (nand_4_out, a, nand_2_out);
  nand nand_5 (nand_5_out, nand_2_out, b);
  nand nand_6 (s0, nand_4_out, nand_5_out);
endmodule
