// Logisim project Guia 03_03.circ as structural Verilog: 1 circuit, main circuit main
module main (
  input  a,
  input  b,
  output s1,
  output out_4
);

  wire nand_2_out, nand_3_out, nand_4_out, nand_5_out, nand_6_out;

  // NAND_Gate nand_1 has open pins: in1=a, in3=b, out=open
  nand nand_2 (nand_2_out, a, a);
  nand nand_3 (nand_3_out, a, b);
  nand nand_4 (nand_4_out, b, nand_2_out);
  nand nand_5 (nand_5_out, a, nand_3_out);
  nand nand_6 (nand_6_out, nand_3_out, b);
  nand nand_7 (s1, nand_4_out, nand_4_out);
  nand nand_8 (out_4, nand_5_out, nand_6_out);

  // Notes on the sheet:
  //   s2
  //   s6
  //   s3
  //   s7
  //   s5
  //   s1
  //   s4
endmodule
