// Logisim project Guia 03_04.circ as structural Verilog: 1 circuit, main circuit main
module main (
  input  a,
  input  b,
  output s1,
  output s0
);

  wire nor_1_out, nor_2_out, nor_3_out;

  nor nor_1 (nor_1_out, a, a);
  nor nor_2 (nor_2_out, b, b);
  nor nor_3 (nor_3_out, a, b);
  nor nor_4 (s1, nor_1_out, nor_2_out);
  nor nor_5 (s0, s1, nor_3_out);

  // Notes on the sheet:
  //   s2
  //   s3
  //   s1
  //   s4
endmodule
