// Logisim project 01.circ as structural Verilog: 1 circuit, main circuit main
module main (
  input  a,
  input  b,
  output s0,
  output s1
);

  xor XOR (s0, a, b);
  and AND (s1, a, b);

  // Notes on the sheet:
  //   Caio Ragacci Pimentel
  //   Meio Somador
endmodule
