// Logisim project exercicio_02.circ as structural Verilog: 1 circuit, main circuit main
module main (
  input  a,
  input  b,
  output s1,
  output s1_2
);

  wire not_1_out, or_1_out;

  and and_1 (s1, a, b);
  or or_1 (or_1_out, b, a);
  not not_1 (not_1_out, s1);
  and and_2 (s1_2, not_1_out, or_1_out);
endmodule
