// Logisim project exercicio_03.circ as structural Verilog: 1 circuit, main circuit main
module main (
  input  a,
  input  b,
  output s0,
  output s1
);

  wire not_1_out;

  not not_1 (not_1_out, a);
  and and_1 (s1, not_1_out, b);
  xor xor_1 (s0, a, b);
endmodule
