// Logisim project 02.circ as structural Verilog: 1 circuit, main circuit main
module main (
  input  in_1,
  input  in_2,
  input  in_3,
  input  in_4,
  output out_5,
  output out_6,
  output out_7,
  output out_8
);

  wire nand_1_out, nand_2_out, nand_3_out, nand_4_out, nand_5_out, nand_6_out, not_1_out, or_1_out;

  nand nand_1 (nand_1_out, in_3, in_3);
  nand nand_2 (nand_2_out, in_4, in_4);
  nand nand_3 (nand_3_out, in_4, in_3);
  or or_1 (or_1_out, in_2, in_1);
  not not_1 (not_1_out, out_6);
  and and_1 (out_6, in_2, in_1);
  nand nand_4 (nand_4_out, out_8, out_8);
  and and_2 (out_5, or_1_out, not_1_out);
  nand nand_5 (nand_5_out, nand_1_out, nand_2_out);
  nand nand_6 (nand_6_out, nand_5_out, nand_4_out);
  nand nand_7 (out_8, nand_3_out, nand_3_out);
  nand nand_8 (out_7, nand_6_out, nand_6_out);
endmodule
