// Logisim project 03.circ as structural Verilog: 1 circuit, main circuit main
module main (
  input  p,
  input  q,
  output s0,
  output s1
);

  wire nand_1_out, nand_2_out, nand_3_out, nand_4_out, nand_5_out;

  nand nand_1 (nand_1_out, p, p);
  nand nand_2 (nand_2_out, q, q);
  nand nand_3 (nand_3_out, p, q);
  nand nand_4 (nand_4_out, nand_1_out, q);
  nand nand_5 (nand_5_out, nand_2_out, p);
  nand nand_6 (s1, nand_3_out, nand_3_out);
  nand nand_7 (s0, nand_4_out, nand_5_out);
endmodule
