// Logisim project meiadiferencanand.circ as structural Verilog: 1 circuit, main circuit main
module main (
  input  a,
  input  b,
  output e1,
  output s
);

  wire tem1_out, tem2_out, tem3_out, tem4_out, tem5_out, tem6_out, tem7_out, tem8_out, x_out, y_out;

  nand tem1 (tem1_out, a, a);
  nand tem2 (tem2_out, b, b);
  nand tem4 (tem4_out, a, b);
  nand y (y_out, b, tem1_out);
  nand tem3 (tem3_out, tem1_out, tem2_out);
  nand x (x_out, tem4_out, tem4_out);
  nand tem5 (tem5_out, tem3_out, tem3_out);
  nand tem6 (tem6_out, x_out, x_out);
  nand u_e1 (e1, y_out, y_out);
  nand tem7 (tem7_out, tem5_out, tem6_out);
  nand tem8 (tem8_out, tem7_out, tem6_out);
  nand u_s (s, tem8_out, tem8_out);

  // Notes on the sheet:
  //   Guia 03 - Capitulo 3  /  Karen Alves Pereira  /  407451                                                                     
  //   Meia- Diferenca com portas NAND
endmodule
