// Logisim project meiadiferencanor.circ as structural Verilog: 1 circuit, main circuit main
module main (
  input  a,
  input  b,
  output e1,
  output s
);

  wire tem1_out, tem3_out, tem4_out, tem5_out, x_out, y_out;

  nor tem1 (tem1_out, b, b);
  nor y (y_out, a, a);
  nor tem3 (tem3_out, a, b);
  nor u_e1 (e1, a, tem1_out);
  nor x (x_out, tem1_out, y_out);
  nor tem4 (tem4_out, tem3_out, tem3_out);
  nor tem5 (tem5_out, tem4_out, tem4_out);
  nor u_s (s, x_out, tem5_out);

  // Notes on the sheet:
  //   Meia-Diferenca com portas NOR
  //   Guia 03 - Capitulo 3 /  Karen Alves Pereira /  407451
endmodule
