// Logisim project meiasoma.circ as structural Verilog: 1 circuit, main circuit main
module main (
  input  a,
  input  b,
  output s,
  output v1
);

  wire not_1_out, or_1_out;

  or or_1 (or_1_out, a, b);
  and and_1 (v1, a, b);
  not not_1 (not_1_out, v1);
  and and_2 (s, or_1_out, not_1_out);

  // Notes on the sheet:
  //   Meia-Soma
  //   Guia 03 - Capitulo 3  / Karen Alves Pereira  / 407451
endmodule
