// Logisim project meiasomanand.circ as structural Verilog: 1 circuit, main circuit main
module main (
  input  a,
  input  b,
  output s,
  output v1
);

  wire tem1_out, tem2_out, tem3_out, tem4_out, tem6_out, tem7_out, tem8_out, tem9_out;

  nand tem1 (tem1_out, a, a);
  nand tem2 (tem2_out, b, b);
  nand tem4 (tem4_out, a, b);
  nand tem3 (tem3_out, tem1_out, tem2_out);
  nand u_v1 (v1, tem4_out, tem4_out);
  nand tem6 (tem6_out, tem3_out, tem3_out);
  nand tem7 (tem7_out, v1, v1);
  nand tem8 (tem8_out, tem6_out, tem7_out);
  nand tem9 (tem9_out, tem8_out, tem7_out);
  nand u_s (s, tem9_out, tem9_out);

  // Notes on the sheet:
  //   Meia-soma com portas NAND
  //   Guia 03 - Capitulo 3  /  Karen Alves Pereira  /  407451                                                                                                                   
endmodule
