// Logisim project guia03exercicio01.circ as structural Verilog: 1 circuit, main circuit main
module main (
  input  A,
  input  B,
  output soma,
  output Carry
);

  wire not_1_out, or_1_out;

  or or_1 (or_1_out, A, B);
  not not_1 (not_1_out, Carry);
  and and_1 (Carry, B, A);
  and and_2 (soma, or_1_out, not_1_out);
endmodule
