// Logisim project guia03exercicio02.circ as structural Verilog: 1 circuit, main circuit main
module main (
  input  a,
  input  b,
  output Soma,
  output Carry_out
);

  wire nand_1_out, nand_2_out, nand_3_out, nand_4_out, nand_6_out;

  nand nand_1 (nand_1_out, a, a);
  nand nand_2 (nand_2_out, b, b);
  nand nand_3 (nand_3_out, a, b);
  nand nand_4 (nand_4_out, nand_1_out, nand_2_out);
  nand nand_5 (Carry_out, nand_3_out, nand_3_out);
  nand nand_6 (nand_6_out, nand_4_out, nand_3_out);
  nand nand_7 (Soma, nand_6_out, nand_6_out);

  // Notes on the sheet:
  //   Larissa Fernandes Leijoto-410476/ Meia soma guia3exercicio02
endmodule
