// Logisim project guia03exercicio03.circ as structural Verilog: 1 circuit, main circuit main
module main (
  input  a,
  input  b,
  output Soma,
  output Carry_out
);

  wire nand_1_out, nand_2_out, nand_3_out, nand_4_out, nand_5_out;

  nand nand_1 (nand_1_out, a, b);
  nand nand_2 (nand_2_out, a, a);
  nand nand_3 (nand_3_out, a, nand_1_out);
  nand nand_4 (nand_4_out, nand_1_out, b);
  nand nand_5 (nand_5_out, b, nand_2_out);
  nand nand_6 (Soma, nand_3_out, nand_4_out);
  nand nand_7 (Carry_out, nand_5_out, nand_5_out);

  // Notes on the sheet:
  //   Larissa fernandes Leijoto-410476/guia03exercicio03
endmodule
