// Logisim project guia03exercicio04extra.circ as structural Verilog: 1 circuit, main circuit main
module main (
  input  a,
  input  b,
  output Soma,
  output Carry
);

  wire nor_1_out, nor_2_out, nor_3_out, nor_4_out, nor_6_out, nor_7_out, nor_8_out;

  nor nor_1 (nor_1_out, a, b);
  nor nor_2 (nor_2_out, a, a);
  nor nor_3 (nor_3_out, b, b);
  nor nor_4 (nor_4_out, nor_1_out, nor_1_out);
  nor nor_5 (Carry, nor_2_out, nor_3_out);
  nor nor_6 (nor_6_out, Carry, Carry);
  nor nor_7 (nor_7_out, nor_4_out, nor_4_out);
  nor nor_8 (nor_8_out, nor_6_out, nor_6_out);
  nor nor_9 (Soma, nor_7_out, nor_8_out);

  // Notes on the sheet:
  //   Larissa Fernandes Leijoto-410476 /Guia03exercicio04extra
endmodule
