// Logisim project guia03exercicio05extra.circ as structural Verilog: 1 circuit, main circuit main
module main (
  input  a,
  input  b,
  output Diferenca,
  output Sinal
);

  wire nor_1_out, nor_2_out, nor_3_out, nor_4_out, nor_5_out, nor_6_out;

  nor nor_1 (nor_1_out, a, a);
  nor nor_2 (nor_2_out, b, b);
  nor nor_3 (nor_3_out, b, a);
  nor nor_4 (nor_4_out, b, b);
  nor nor_5 (nor_5_out, nor_1_out, nor_1_out);
  nor nor_6 (nor_6_out, nor_1_out, nor_2_out);
  nor nor_7 (Sinal, nor_4_out, nor_5_out);
  nor nor_8 (Diferenca, nor_6_out, nor_3_out);

  // Notes on the sheet:
  //   Larissa Fernandes Leijoto -410476 /Guia3exercicio05
endmodule
