// Logisim project Meia soma trad nor.circ as structural Verilog: 1 circuit, main circuit main
module main (
  input  x,
  input  y,
  output s,
  output s0
);

  wire nor_1_out, nor_2_out, nor_3_out, nor_4_out, nor_5_out, nor_6_out, nor_7_out, nor_8_out, nor_9_out,
       nor_10_out, nor_11_out;

  not nor_1 (nor_1_out, x);  // NOR_Gate
  not nor_2 (nor_2_out, y);  // NOR_Gate
  nor nor_3 (nor_3_out, nor_1_out, nor_1_out);
  nor nor_4 (nor_4_out, y, y);
  nor nor_5 (nor_5_out, nor_2_out, nor_2_out);
  nor nor_6 (nor_6_out, x, x);
  nor nor_7 (nor_7_out, nor_3_out, nor_4_out);
  nor nor_8 (nor_8_out, nor_5_out, nor_6_out);
  nor nor_9 (nor_9_out, y, y);
  nor nor_10 (nor_10_out, x, x);
  nor nor_11 (nor_11_out, nor_7_out, nor_8_out);
  nor nor_12 (s, nor_11_out, nor_11_out);
  nor nor_13 (s0, nor_9_out, nor_10_out);

  // Notes on the sheet:
  //   Jessica Luisa Betonico Andrade -  412748
  //   Meia soma com nor
  //   tmp
  //   tmp4
  //   tmp1
  //   tmp2
  //   tmp5
  //   tmp6
  //   tmp3
  //   tmp7
  //   tmp10
  //   tmp8
  //   tmp9
endmodule
