// Logisim project meia soma trad.circ as structural Verilog: 1 circuit, main circuit main
module main (
  input  x,
  input  y,
  output s,
  output s0
);

  wire and_2_out, and_3_out, not_1_out, not_2_out;

  not not_1 (not_1_out, x);
  not not_2 (not_2_out, y);
  and and_1 (s0, y, x);
  and and_2 (and_2_out, not_1_out, y);
  and and_3 (and_3_out, x, not_2_out);
  or or_1 (s, and_2_out, and_3_out);

  // Notes on the sheet:
  //   meia soma tradicional
  //   Jessica Luisa Betonico Andrade -  412748
endmodule
