// Logisim project circuito01.circ as structural Verilog: 1 circuit, main circuit main
module main (
  input  a,
  input  b,
  output s2,
  output s1
);

  wire not_1_out, or_1_out;

  and and_1 (s2, a, b);
  or or_1 (or_1_out, b, a);
  not not_1 (not_1_out, s2);
  and and_2 (s1, not_1_out, or_1_out);

  // Notes on the sheet:
  //   s3
  //   s4
endmodule
