// Logisim project circuito02.circ as structural Verilog: 1 circuit, main circuit main
module main (
  input  p,
  input  q,
  output s0,
  output s1
);

  wire nand_1_out, nand_2_out, nand_4_out, nand_6_out;

  nand nand_1 (nand_1_out, p, q);
  nand nand_2 (nand_2_out, p, nand_1_out);
  nand nand_3 (nand_2_out, nand_1_out, q);
  nand nand_4 (nand_4_out, nand_1_out, nand_1_out);
  not nand_5 (s0, nand_2_out);  // NAND_Gate
  nand nand_6 (nand_6_out, nand_4_out, nand_4_out);
  nand nand_7 (s1, nand_6_out, nand_6_out);

  // Notes on the sheet:
  //   s2
  //   s4
  //   s3
  //   s5
  //   s6
endmodule
