// Logisim project 02.circ as structural Verilog: 1 circuit, main circuit main
module main (
  input  a,
  input  b,
  output s0,
  output s1
);

  wire nand_1_out, nand_2_out, nand_3_out, nand_4_out, nand_5_out, nand_6_out, nand_7_out;

  nand nand_1 (nand_1_out, a, b);
  nand nand_2 (nand_2_out, a, b);
  nand nand_3 (nand_3_out, nand_2_out, nand_2_out);
  nand nand_4 (nand_4_out, a, nand_1_out);
  nand nand_5 (nand_5_out, nand_1_out, b);
  nand nand_6 (nand_6_out, nand_3_out, nand_3_out);
  nand nand_7 (nand_7_out, nand_3_out, nand_3_out);
  nand XOR (s0, nand_4_out, nand_5_out);
  nand nand_8 (s1, nand_6_out, nand_7_out);

  // Notes on the sheet:
  //   Silvino Henrique Santos de Souza
  //   Meia Soma usando portas NAND
endmodule
