// Logisim project guia03-1.circ as structural Verilog: 1 circuit, main circuit main
module main (
  input  in_1,
  input  b,
  output s0,
  output s1
);

  wire nand_1_out, or_1_out;

  or or_1 (or_1_out, in_1, b);
  nand nand_1 (nand_1_out, in_1, b);
  and and_1 (s1, in_1, b);
  and and_2 (s0, or_1_out, nand_1_out);
endmodule
