// Logisim project guia03-2.circ as structural Verilog: 1 circuit, main circuit main
module main (
  input  in_1,
  input  in_2,
  output s0,
  output s1
);

  wire nand_1_out, nand_2_out, nand_3_out, nand_5_out;

  nand nand_1 (nand_1_out, in_1, in_2);
  nand nand_2 (nand_2_out, in_1, in_2);
  nand nand_3 (nand_3_out, nand_2_out, in_2);
  nand nand_4 (s0, nand_1_out, nand_1_out);
  nand nand_5 (nand_5_out, in_1, nand_2_out);
  nand nand_6 (s1, nand_5_out, nand_5_out, nand_3_out);
endmodule
