// Logisim project guia03-3.circ as structural Verilog: 1 circuit, main circuit main
module main (
  input  in_1,
  input  in_2,
  output out_3,
  output out_4
);

  wire temp3_out, temp4_out, temp5_out, temp6_out, temp7_out;

  // NAND_Gate temp2 has open pins: in0=in_1, in3=in_2, out=open
  nand temp6 (temp6_out, in_1, in_1);
  nand temp3 (temp3_out, in_2, in_1);
  nand temp7 (temp7_out, in_2, temp6_out);
  not temp4 (temp4_out, in_1);  // NAND_Gate
  nand temp5 (temp5_out, in_2, temp3_out);
  not temp1 (out_3, temp7_out);  // NAND_Gate
  nand nand_1 (out_4, temp4_out, temp3_out, temp5_out);
endmodule
