// Logisim project guia03-4.circ as structural Verilog: 1 circuit, main circuit main
module main (
  input  a,
  input  b,
  output s1,
  output s0
);

  wire s2_out, s3_out, s4_out;

  nor s2 (s2_out, a, a);
  nor s3 (s3_out, b, b);
  nor s4 (s4_out, a, b);
  nor u_s1 (s1, s2_out, s3_out);
  nor nor_1 (s0, s1, s4_out);
endmodule
