// Logisim project Exercicio 01.circ as structural Verilog: 1 circuit, main circuit main
module main (
  input  A,
  input  B,
  output s0,
  output s1
);

  wire and_1_out, and_2_out, not_1_out, not_2_out;

  not not_1 (not_1_out, A);
  not not_2 (not_2_out, B);
  and and_1 (and_1_out, not_1_out, B);
  and and_2 (and_2_out, A, not_2_out);
  or or_1 (s0, and_1_out, and_2_out);
  and and_3 (s1, A, B);

  // Notes on the sheet:
  //   Bruno César Lopes Silva - 415985
endmodule
