// Logisim project Exercicio 02.circ as structural Verilog: 1 circuit, main circuit main
module main (
  input  A,
  input  B,
  output s,
  output s0
);

  wire nand_1_out, nand_2_out, nand_3_out, nand_4_out, nand_5_out;

  nand nand_1 (nand_1_out, A, A);
  nand nand_2 (nand_2_out, B, B);
  nand nand_3 (nand_3_out, B, A);
  nand nand_4 (nand_4_out, nand_1_out, B);
  nand nand_5 (nand_5_out, A, nand_2_out);
  nand nand_6 (s0, nand_3_out, nand_3_out);
  nand nand_7 (s, nand_4_out, nand_5_out);

  // Notes on the sheet:
  //   Bruno César Lopes Silva - 415985
endmodule
