// Logisim project Exercicio 04.circ as structural Verilog: 1 circuit, main circuit main
module main (
  input  a,
  input  b,
  output s,
  output s0
);

  wire nor_1_out, nor_2_out, nor_3_out, nor_4_out, nor_5_out;

  nor nor_1 (nor_1_out, a, a);
  nor nor_2 (nor_2_out, b, b);
  nor nor_3 (nor_3_out, nor_1_out, b);
  nor nor_4 (nor_4_out, a, nor_2_out);
  nor nor_5 (nor_5_out, nor_3_out, nor_4_out);
  nor nor_6 (s, nor_5_out, nor_5_out);
  nor nor_7 (s0, nor_1_out, nor_2_out);

  // Notes on the sheet:
  //   Bruno César Lopes Silva - 415985
endmodule
