// Logisim project Ex_01_Half_Adder.circ as structural Verilog: 1 circuit, main circuit main
module main (
  input  A,
  input  B,
  output s1,
  output s0
);

  and AND1 (s1, A, B);
  xor XOR1 (s0, A, B);

  // Notes on the sheet:
  //   Guia 03_01 - Half Adder
  //   Aluno: Alyson Deives
  //   Matricula: 416589
endmodule
