// Logisim project Ex_02_Half_Adder_nand.circ as structural Verilog: 1 circuit, main circuit main
module main (
  input  A,
  input  B,
  output s1,
  output s0
);

  wire nand_1_out, nand_2_out, nand_3_out, nand_5_out, nand_6_out;

  nand nand_1 (nand_1_out, A, B);
  nand nand_2 (nand_2_out, A, A);
  nand nand_3 (nand_3_out, B, B);
  nand nand_4 (s1, nand_1_out, nand_1_out);
  nand nand_5 (nand_5_out, nand_2_out, B);
  nand nand_6 (nand_6_out, nand_3_out, A);
  nand nand_7 (s0, nand_5_out, nand_6_out);

  // Notes on the sheet:
  //   Guia 03_02 - Half Adder with NAND gates
  //   Aluno: Alyson Deives
  //   Matricula: 416589
endmodule
