// Logisim project Ex_03_Half_Differ_nand.circ as structural Verilog: 1 circuit, main circuit main
module main (
  input  A,
  input  B,
  output s1,
  output s0
);

  wire nand_1_out, nand_2_out, nand_3_out, nand_4_out, nand_5_out, nand_6_out;

  nand nand_1 (nand_1_out, A, A);
  nand nand_2 (nand_2_out, A, A);
  nand nand_3 (nand_3_out, B, B);
  nand nand_4 (nand_4_out, nand_1_out, B);
  nand nand_5 (nand_5_out, nand_2_out, B);
  nand nand_6 (nand_6_out, nand_3_out, A);
  nand nand_7 (s1, nand_4_out, nand_4_out);
  nand nand_8 (s0, nand_5_out, nand_6_out);

  // Notes on the sheet:
  //   Aluno: Alyson Deives
  //   Matricula: 416589
  //   Guia 03_03 - Half Differ with NAND gates
endmodule
