// Logisim project Ex_04_Half_Adder_nor.circ as structural Verilog: 1 circuit, main circuit main
module main (
  input  A,
  input  B,
  output s1,
  output s0
);

  wire nor_1_out, nor_2_out, nor_3_out, nor_4_out, nor_6_out, nor_7_out, nor_8_out;

  nor nor_1 (nor_1_out, A, A);
  nor nor_2 (nor_2_out, B, B);
  nor nor_3 (nor_3_out, A, A);
  nor nor_4 (nor_4_out, B, B);
  nor nor_5 (s1, nor_1_out, nor_2_out);
  nor nor_6 (nor_6_out, nor_3_out, B);
  nor nor_7 (nor_7_out, nor_4_out, A);
  nor nor_8 (nor_8_out, nor_6_out, nor_7_out);
  nor nor_9 (s0, nor_8_out, nor_8_out);

  // Notes on the sheet:
  //   Aluno: Alyson Deives
  //   Matricula: 416589
  //   Guia 03_05 - Half Adder with NOR gates
endmodule
