// Logisim project Meia diferença Comp nand.circ as structural Verilog: 1 circuit, main circuit main
module main (
  input  x,
  input  y,
  output d,
  output Vem1
);

  wire nand_1_out, nand_2_out, nand_3_out, nand_4_out, nand_5_out, nand_6_out, nand_8_out, nand_9_out,
       nand_10_out, nand_11_out;

  nand nand_1 (nand_1_out, x, x);
  not nand_2 (nand_2_out, y);  // NAND_Gate
  not nand_3 (nand_3_out, x);  // NAND_Gate
  nand nand_4 (nand_4_out, nand_1_out, y);
  nand nand_5 (nand_5_out, nand_3_out, y);
  nand nand_6 (nand_6_out, x, nand_2_out);
  nand nand_7 (Vem1, nand_4_out, nand_4_out);
  nand nand_8 (nand_8_out, nand_5_out, nand_5_out);
  nand nand_9 (nand_9_out, nand_6_out, nand_6_out);
  nand nand_10 (nand_10_out, nand_8_out, nand_8_out);
  nand nand_11 (nand_11_out, nand_9_out, nand_9_out);
  nand nand_12 (d, nand_10_out, nand_11_out);

  // Notes on the sheet:
  //   t8
  //   meia diferença de nand
  //   t0
  //   t4
  //   t9
  //   t1
  //   t5
  //   t2
  //   t6
  //   t3
  //   t7
endmodule
