// Logisim project Meia diferença Comp nor.circ as structural Verilog: 1 circuit, main circuit main
module main (
  input  x,
  input  y,
  output d,
  output Vai1
);

  wire nor_1_out, nor_2_out, nor_3_out, nor_4_out, nor_5_out, nor_6_out, nor_7_out, nor_8_out, nor_9_out,
       nor_10_out, nor_11_out, nor_12_out;

  not nor_1 (nor_1_out, x);  // NOR_Gate
  nor nor_2 (nor_2_out, y, y);
  nor nor_3 (nor_3_out, nor_1_out, nor_1_out);
  nor nor_4 (nor_4_out, y, y);
  nor nor_5 (nor_5_out, nor_2_out, nor_2_out);
  nor nor_6 (nor_6_out, x, x);
  nor nor_7 (nor_7_out, x, x);
  nor nor_8 (nor_8_out, nor_3_out, nor_4_out);
  nor nor_9 (nor_9_out, nor_5_out, nor_6_out);
  nor nor_10 (nor_10_out, y, y);
  nor nor_11 (nor_11_out, nor_8_out, nor_9_out);
  nor nor_12 (nor_12_out, nor_7_out, nor_7_out);
  nor nor_13 (d, nor_11_out, nor_11_out);
  nor nor_14 (Vai1, nor_10_out, nor_12_out);

  // Notes on the sheet:
  //   Meia diferença com nor
  //   t0
  //   t4
  //   t1
  //   t2
  //   t5
  //   t6
  //   t9
  //   t3
  //   t7
  //   t8
  //   t10
  //   t11
endmodule
