// Logisim project Meia soma trad nand.circ as structural Verilog: 1 circuit, main circuit main
module main (
  input  x,
  input  y,
  output s,
  output Vout
);

  wire nand_1_out, nand_2_out, nand_3_out, nand_4_out, nand_5_out, nand_6_out, nand_8_out, nand_9_out,
       nand_10_out;

  nand nand_1 (nand_1_out, y, y);
  nand nand_2 (nand_2_out, x, x);
  nand nand_3 (nand_3_out, x, nand_1_out);
  nand nand_4 (nand_4_out, y, x);
  nand nand_5 (nand_5_out, nand_2_out, y);
  nand nand_6 (nand_6_out, nand_3_out, nand_3_out);
  nand nand_7 (Vout, nand_4_out, nand_4_out);
  nand nand_8 (nand_8_out, nand_5_out, nand_5_out);
  nand nand_9 (nand_9_out, nand_8_out, nand_8_out);
  nand nand_10 (nand_10_out, nand_6_out, nand_6_out);
  nand nand_11 (s, nand_9_out, nand_10_out);

  // Notes on the sheet:
  //   not
  //   not
  //   temp4
  //   temp0
  //   temp5
  //   and
  //   and
  //   temp8
  //   meia soma de nand
  //   and
  //   temp1
  //   temp6
  //   temp2
  //   Or
  //   temp3
  //   temp7
endmodule
