// Logisim project guia3_4_Logisim.circ as structural Verilog: 1 circuit, main circuit main
module main (
  input  A,
  input  B,
  output out_3,
  output out_4
);

  wire Nor1_out, Nor2_out, Nor3_out, Nor4_out, Nor6_out, Nor7_out;

  nor Nor1 (Nor1_out, A, A);
  nor Nor2 (Nor2_out, B, B);
  nor Nor6 (Nor6_out, B, B);
  nor Nor7 (Nor7_out, A, A);
  nor Nor3 (Nor3_out, Nor1_out, Nor2_out);
  nor Nor4 (Nor4_out, B, A);
  nor Nor8 (out_4, Nor6_out, Nor7_out);
  nor Nor5 (out_3, Nor3_out, Nor4_out);
endmodule
