// Logisim project guia3_5_Logisim.circ as structural Verilog: 1 circuit, main circuit main
module main (
  input  A,
  input  B,
  output out_3,
  output out_4
);

  wire Nor1_out, Nor2_out, Nor3_out, Nor4_out, Nor6_out, Nor7_out, Not_de_Nor_out;

  nor Nor1 (Nor1_out, A, A);
  nor Nor2 (Nor2_out, B, B);
  nor Not_de_Nor (Not_de_Nor_out, A, A);
  nor Nor3 (Nor3_out, Nor1_out, Nor2_out);
  nor Nor4 (Nor4_out, B, A);
  nor Nor6 (Nor6_out, B, B);
  nor Nor7 (Nor7_out, Not_de_Nor_out, Not_de_Nor_out);
  nor Nor5 (out_3, Nor3_out, Nor4_out);
  nor Nor8 (out_4, Nor6_out, Nor7_out);
endmodule
