// Logisim project Guia03.circ as structural Verilog: 5 circuits, main circuit Ex01 - Half Adder
module Ex01___Half_Adder (
  input  a,
  input  b,
  output Soma,
  output Cout
);

  wire not_1_out, or_1_out;

  or or_1 (or_1_out, a, b);
  and and_1 (Cout, b, a);
  not not_1 (not_1_out, Cout);
  and and_2 (Soma, or_1_out, not_1_out);

  // Notes on the sheet:
  //   Douglas de Loredo Borges - 417889
endmodule

module Ex02___Half_Adder (
  input  a,
  input  b,
  output Soma,
  output Cout
);

  wire nand_1_out, nand_2_out, nand_3_out, nand_4_out, nand_5_out;

  nand nand_1 (nand_1_out, a, a);
  nand nand_2 (nand_2_out, b, b);
  nand nand_3 (nand_3_out, b, a);
  nand nand_4 (nand_4_out, nand_1_out, nand_2_out);
  nand nand_5 (nand_5_out, nand_4_out, nand_3_out);
  nand nand_6 (Cout, nand_3_out, nand_3_out);
  nand nand_7 (Soma, nand_5_out, nand_5_out);

  // Notes on the sheet:
  //   Douglas de Loredo Borges - 417889
endmodule

module Ex03___Half_Subtractor (
  input  a,
  input  b,
  output \Subtração ,
  output Vin
);

  wire nand_1_out, nand_2_out, nand_3_out, nand_4_out, nand_5_out;

  nand nand_1 (nand_1_out, a, b);
  nand nand_2 (nand_2_out, a, a);
  nand nand_3 (nand_3_out, a, nand_1_out);
  nand nand_4 (nand_4_out, nand_1_out, b);
  nand nand_5 (nand_5_out, b, nand_2_out);
  nand nand_6 (\Subtração , nand_3_out, nand_4_out);
  nand nand_7 (Vin, nand_5_out, nand_5_out);

  // Notes on the sheet:
  //   Douglas de Loredo Borges - 417889
endmodule

module Ex04___Half_Adder (
  input  a,
  input  b,
  output Soma,
  output Cout
);

  wire nor_1_out, nor_2_out, nor_4_out;

  nor nor_1 (nor_1_out, a, b);
  nor nor_2 (nor_2_out, b, b);
  nor nor_3 (Cout, nor_2_out, nor_4_out);
  nor nor_4 (nor_4_out, a, a);
  nor nor_5 (Soma, nor_1_out, Cout);

  // Notes on the sheet:
  //   Douglas de Loredo Borges - 417889
endmodule

module Ex05___Half_Subtractor (
  input  a,
  input  b,
  output \Subtração ,
  output Vin
);

  wire nor_1_out, nor_2_out, nor_3_out, nor_4_out, nor_5_out;

  nor nor_1 (nor_1_out, a, a);
  nor nor_2 (nor_2_out, nor_1_out, nor_3_out);
  nor nor_3 (nor_3_out, b, b);
  nor nor_4 (nor_4_out, a, b);
  nor nor_5 (nor_5_out, b, b);
  nor nor_6 (Vin, nor_5_out, a);
  nor nor_7 (\Subtração , nor_2_out, nor_4_out);

  // Notes on the sheet:
  //   Douglas de Loredo Borges - 417889
endmodule
