// Logisim project meio-somador.circ as structural Verilog: 1 circuit, main circuit main
module main (
  input  A,
  input  B,
  output S,
  output Carry_out
);

  wire and_2_out, and_3_out, not_1_out, not_2_out;

  not not_1 (not_1_out, A);
  not not_2 (not_2_out, B);
  and and_1 (Carry_out, A, B);
  and and_2 (and_2_out, not_1_out, B);
  and and_3 (and_3_out, not_2_out, A);
  or or_1 (S, and_2_out, and_3_out);
endmodule
