// Logisim project meio-subtrator_nand.circ as structural Verilog: 1 circuit, main circuit main
module main (
  input  A,
  input  B,
  output S,
  output Borrow_out
);

  wire nand_1_out, nand_2_out, nand_3_out, nand_4_out, nand_5_out;

  nand nand_1 (nand_1_out, A, A);
  nand nand_2 (nand_2_out, B, B);
  nand nand_3 (nand_3_out, nand_1_out, B);
  nand nand_4 (nand_4_out, nand_2_out, A);
  nand nand_5 (nand_5_out, nand_1_out, B);
  nand nand_6 (S, nand_3_out, nand_4_out);
  nand nand_7 (Borrow_out, nand_5_out, nand_5_out);
endmodule
