// Logisim project exercicio01.circ as structural Verilog: 1 circuit, main circuit exercicio01
module exercicio01 (
  input  e1,
  input  e2,
  output saida,
  output carry
);

  wire not_1_out, or_1_out;

  or or_1 (or_1_out, e1, e2);
  not not_1 (not_1_out, carry);
  and and_1 (carry, e1, e2);
  and and_2 (saida, or_1_out, not_1_out);

  // Notes on the sheet:
  //   Isabella Gonçales - 420120
  //   temp1
  //   temp2
endmodule
