// Logisim project exercicio02.circ as structural Verilog: 1 circuit, main circuit exercicio02
module exercicio02 (
  input  e1,
  input  e2,
  output saida,
  output carry
);

  wire nand_1_out, nand_2_out, nand_3_out, nand_4_out, nand_6_out;

  nand nand_1 (nand_1_out, e1, e1);
  nand nand_2 (nand_2_out, e2, e2);
  nand nand_3 (nand_3_out, e1, e1, e2);
  nand nand_4 (nand_4_out, nand_1_out, nand_2_out);
  not nand_5 (carry, nand_3_out);  // NAND_Gate
  nand nand_6 (nand_6_out, nand_4_out, nand_3_out);
  not nand_7 (saida, nand_6_out);  // NAND_Gate

  // Notes on the sheet:
  //   temp1
  //   temp2
  //   temp3
  //   temp4
  //   Isabella Gonçales - 420120
  //   temp5
endmodule
