// Logisim project exercicio03.circ as structural Verilog: 1 circuit, main circuit main
module main (
  input  e1,
  input  e2,
  output saida,
  output sinal
);

  wire nand_1_out, nand_2_out, nand_3_out, nand_4_out, nand_5_out;

  nand nand_1 (nand_1_out, e2, e1);
  nand nand_2 (nand_2_out, e1, e1);
  nand nand_3 (nand_3_out, e1, nand_1_out);
  nand nand_4 (nand_4_out, nand_1_out, e2);
  nand nand_5 (nand_5_out, e2, nand_2_out);
  nand nand_6 (saida, nand_3_out, nand_4_out);
  nand nand_7 (sinal, nand_5_out, nand_5_out);

  // Notes on the sheet:
  //   temp1
  //   temp4
  //   Isabella Gonçales - 420120
  //   temp2
  //   temp3
  //   temp5
endmodule
