// Logisim project exercicio04.circ as structural Verilog: 1 circuit, main circuit main
module main (
  input  e1,
  input  e2,
  output saida,
  output carry
);

  wire nor_1_out, nor_2_out, nor_3_out;

  nor nor_1 (nor_1_out, e2, e1);
  nor nor_2 (nor_2_out, e1, e1);
  nor nor_3 (nor_3_out, e2, e2);
  nor nor_4 (carry, nor_2_out, nor_3_out);
  nor nor_5 (saida, nor_1_out, carry);

  // Notes on the sheet:
  //   temp2
  //   temp3
  //   temp1
  //   Isabella Gonçales - 420120
endmodule
