// Logisim project exercicio05.circ as structural Verilog: 1 circuit, main circuit main
module main (
  input  e1,
  input  e2,
  output saida,
  output sinal
);

  wire nor_1_out, nor_2_out, nor_3_out, nor_4_out, nor_5_out, nor_6_out;

  nor nor_1 (nor_1_out, e2, e2);
  nor nor_2 (nor_2_out, e1, e1);
  nor nor_3 (nor_3_out, e2, e1);
  nor nor_4 (nor_4_out, e2, e2);
  nor nor_5 (nor_5_out, nor_1_out, nor_2_out);
  nor nor_6 (nor_6_out, nor_5_out, nor_3_out);
  nor nor_7 (sinal, nor_4_out, e1);
  nor nor_8 (saida, nor_6_out, nor_6_out);

  // Notes on the sheet:
  //   temp2
  //   temp1
  //   temp4
  //   temp3
  //   temp6
  //   Isabella Gonçales - 420120
  //   temp5
endmodule
