// Logisim project cir..circ as structural Verilog: 5 circuits, main circuit Exercicio01
module Exercicio01 (
  input  a,
  input  b,
  output s0,
  output s1
);

  wire not_1_out, or_1_out;

  or or_1 (or_1_out, a, b);
  and and_1 (s1, a, a);
  not not_1 (not_1_out, s1);
  and and_2 (s0, or_1_out, not_1_out);

  // Notes on the sheet:
  //   Operador De Meia-Soma
endmodule

module Exercicio02 (
  input  a,
  input  b,
  output s0,
  output s1
);

  wire nand_1_out, nand_2_out, nand_3_out, nand_4_out, nand_6_out;

  nand nand_1 (nand_1_out, a, a);
  nand nand_2 (nand_2_out, b, b);
  nand nand_3 (nand_3_out, a, b);
  nand nand_4 (nand_4_out, nand_1_out, nand_2_out);
  nand nand_5 (s1, nand_3_out, nand_3_out);
  nand nand_6 (nand_6_out, nand_4_out, nand_3_out);
  nand nand_7 (s0, nand_6_out, nand_6_out);

  // Notes on the sheet:
  //   Operador Meia-Soma
endmodule

module exercicio03 (
  input  a,
  input  b,
  output \diferença ,
  output sinal
);

  wire nand_1_out, nand_2_out, nand_3_out, nand_4_out, nand_5_out;

  nand nand_1 (nand_1_out, a, b);
  nand nand_2 (nand_2_out, a, a);
  nand nand_3 (nand_3_out, a, nand_1_out);
  nand nand_4 (nand_4_out, nand_1_out, b);
  nand nand_5 (nand_5_out, b, nand_2_out);
  nand nand_6 (\diferença , nand_3_out, nand_4_out);
  nand nand_7 (sinal, nand_5_out, nand_5_out);

  // Notes on the sheet:
  //   Operador Meia-Diferença
endmodule

module Exercicio04 (
  input  a,
  input  b,
  output s0,
  output s1
);

  wire nor_1_out, nor_2_out, nor_3_out, nor_4_out, nor_6_out, nor_7_out, nor_8_out;

  nor nor_1 (nor_1_out, a, b);
  nor nor_2 (nor_2_out, a, a);
  nor nor_3 (nor_3_out, b, b);
  nor nor_4 (nor_4_out, nor_1_out, nor_1_out);
  nor nor_5 (s1, nor_2_out, nor_3_out);
  nor nor_6 (nor_6_out, s1, s1);
  nor nor_7 (nor_7_out, nor_4_out, nor_4_out);
  nor nor_8 (nor_8_out, nor_6_out, nor_6_out);
  nor nor_9 (s0, nor_7_out, nor_8_out);

  // Notes on the sheet:
  //   Operador Meia-Soma
endmodule

module Exercicio05 (
  input  a,
  input  b,
  output s0,
  output s1
);

  wire nor_1_out, nor_2_out, nor_3_out, nor_4_out, nor_5_out, nor_6_out, nor_7_out;

  nor nor_1 (nor_1_out, a, a);
  nor nor_2 (nor_2_out, b, b);
  nor nor_3 (nor_3_out, a, b);
  nor nor_4 (nor_4_out, b, b);
  nor nor_5 (nor_5_out, nor_1_out, nor_2_out);
  nor nor_6 (nor_6_out, nor_4_out, nor_4_out);
  nor nor_7 (nor_7_out, a, a);
  nor nor_8 (s0, nor_5_out, nor_3_out);
  nor nor_9 (s1, nor_6_out, nor_7_out);

  // Notes on the sheet:
  //   Operador Meia-Diferença
endmodule
