// Logisim project Exemplo0032.circ as structural Verilog: 1 circuit, main circuit main
module main (
  input  in_1,
  input  in_2,
  input  in_3,
  input  in_4,
  input  in_5,
  input  in_6,
  input  in_7,
  input  in_8,
  input  in_9,
  input  in_10,
  input  in_11,
  input  in_12,
  input  in_13
);

  wire and_1_out, or_1_out, or_2_out, undriven, undriven_2;

  and and_1 (and_1_out, undriven, undriven_2);
  or or_1 (or_1_out, in_12, in_12);
  or or_2 (or_2_out, and_1_out, or_1_out);

  assign in_13 = in_12;
endmodule
