// Logisim project Exemplo 01.circ as structural Verilog: 2 circuits, main circuit Meia_Soma_Com_NOR
module Meia_Soma_Com_NOR (
  input  a,
  input  b,
  output s0,
  output s1
);

  wire nor_1_out, nor_2_out, nor_3_out, nor_4_out, nor_6_out, nor_7_out, nor_9_out;

  nor nor_1 (nor_1_out, a, b);
  nor nor_2 (nor_2_out, a, a);
  nor nor_3 (nor_3_out, b, b);
  nor nor_4 (nor_4_out, nor_1_out, nor_1_out);
  nor nor_5 (s1, nor_2_out, nor_3_out);
  nor nor_6 (nor_6_out, s1, s1);
  nor nor_7 (nor_7_out, nor_4_out, nor_4_out);
  nor nor_8 (s0, nor_7_out, nor_9_out);
  nor nor_9 (nor_9_out, nor_6_out, nor_6_out);

  // Notes on the sheet:
  //   Nome: Bruno Rafael Nicolletti - Matrícula: 380752
endmodule

module main (
  input  a,
  input  b,
  output s0,
  output s1
);

  Meia_Soma_Com_NOR meia_soma_com_nor_1 (.a(a), .b(b), .s0(s0), .s1(s1));

  // Notes on the sheet:
  //   Nome: Bruno Rafael Nicolletti - Matrícula: 380752
endmodule
