// Logisim project Exemplo 02.circ as structural Verilog: 2 circuits, main circuit Soma_Completa_com_Meia_Soma
module Soma_Completa_com_Meia_Soma (
  input  c,
  input  a,
  input  b,
  output s0,
  output s1
);

  wire meia_soma_compacto_1_out_3, meia_soma_compacto_1_out_4, meia_soma_compacto_2_out_4;

  Meia_Soma_Compacto meia_soma_compacto_1 (
    .a(a), .b(b), .out_3(meia_soma_compacto_1_out_3), .out_4(meia_soma_compacto_1_out_4));
  Meia_Soma_Compacto meia_soma_compacto_2 (
    .a(c), .b(meia_soma_compacto_1_out_3), .out_3(s0), .out_4(meia_soma_compacto_2_out_4));
  or or_1 (s1, meia_soma_compacto_2_out_4, meia_soma_compacto_1_out_4);

  // Notes on the sheet:
  //   Nome: Bruno Rafael Nicolletti - Matrícula: 380752
endmodule

module Meia_Soma_Compacto (
  input  a,
  input  b,
  output out_3,
  output out_4
);

  xor xor_1 (out_3, a, b);
  and and_1 (out_4, a, b);

  // Notes on the sheet:
  //   Nome: Bruno Rafael Nicolletti - Matrícula: 380752
endmodule
