// Logisim project Exemplo 03.circ as structural Verilog: 2 circuits, main circuit Diferenca_Completa_Com_Meia_Diferenca
module Diferenca_Completa_Com_Meia_Diferenca (
  input  c,
  input  a,
  input  b,
  output s0,
  output s1
);

  wire meia_diferenca_compacto_1_s0, meia_diferenca_compacto_1_s1, meia_diferenca_compacto_2_s1;

  Meia_Diferenca_Compacto meia_diferenca_compacto_1 (
    .a(a), .b(b), .s0(meia_diferenca_compacto_1_s0), .s1(meia_diferenca_compacto_1_s1));
  Meia_Diferenca_Compacto meia_diferenca_compacto_2 (
    .a(meia_diferenca_compacto_1_s0), .b(c), .s0(s0), .s1(meia_diferenca_compacto_2_s1));
  or or_1 (s1, meia_diferenca_compacto_2_s1, meia_diferenca_compacto_1_s1);

  // Notes on the sheet:
  //   Nome: Bruno Rafael Nicolletti - Matrícula: 380752
endmodule

module Meia_Diferenca_Compacto (
  input  a,
  input  b,
  output s0,
  output s1
);

  wire not_1_out;

  not not_1 (not_1_out, a);
  xor xor_1 (s0, a, b);
  and and_1 (s1, b, not_1_out);

  // Notes on the sheet:
  //   Nome: Bruno Rafael Nicolletti - Matrícula: 380752
endmodule
