// Logisim project Guia_0401.circ as structural Verilog: 1 circuit, main circuit main
module main (
  input  a,
  input  b,
  output s1,
  output s0
);

  wire nor_1_out, nor_2_out, nor_3_out, nor_4_out, nor_5_out, nor_6_out;

  nor nor_1 (nor_1_out, a, a);
  nor nor_2 (nor_2_out, b, b);
  nor nor_3 (nor_3_out, b, a);
  nor nor_4 (nor_4_out, b, b);
  nor nor_5 (nor_5_out, a, a);
  nor nor_6 (nor_6_out, nor_1_out, nor_2_out);
  nor nor_7 (s0, nor_4_out, nor_5_out);
  nor nor_8 (s1, nor_6_out, nor_3_out);
endmodule
