// Logisim project Guia_0403.circ as structural Verilog: 1 circuit, main circuit main
module main (
  input  a,
  input  b,
  output out_3,
  output out_4
);

  wire not_1_out;

  not not_1 (not_1_out, a);
  xor xor_1 (out_3, a, b);
  and and_1 (out_4, not_1_out, b);
endmodule
