// Logisim project Guia04Ex02.circ as structural Verilog: 2 circuits, main circuit meia soma
module meia_soma (
  input  a,
  input  b,
  output s0,
  output s1
);

  and and_1 (s0, a, a);
  xor xor_1 (s1, a, a);

  assign b = a;

  // Notes on the sheet:
  //   Alvaro - 395487
endmodule

module somacompleta (
  input  v,
  input  a,
  input  b,
  output s0,
  output s1
);

  wire meia_soma_1_s0, meia_soma_1_s1, meia_soma_2_s1;

  meia_soma meia_soma_1 (.a(a), .b(b), .s0(meia_soma_1_s0), .s1(meia_soma_1_s1));
  meia_soma meia_soma_2 (.a(v), .b(meia_soma_1_s0), .s0(s0), .s1(meia_soma_2_s1));
  or or_1 (s1, meia_soma_2_s1, meia_soma_1_s1);
endmodule
