// Logisim project Guia04Ex03.circ as structural Verilog: 2 circuits, main circuit meiadiferenca
module meiadiferenca (
  input  a,
  input  b,
  output s0,
  output s1
);

  wire not_1_out;

  not not_1 (not_1_out, a);
  and and_1 (s0, not_1_out, b);
  xor xor_1 (s1, b, a);

  // Notes on the sheet:
  //   Alvaro Henrique - 395487
endmodule

module diferencacompleta (
  input  v,
  input  a,
  input  b,
  output s0,
  output s1
);

  wire meiadiferenca_1_s0, meiadiferenca_1_s1, meiadiferenca_2_s1;

  meiadiferenca meiadiferenca_1 (.a(a), .b(b), .s0(meiadiferenca_1_s0), .s1(meiadiferenca_1_s1));
  meiadiferenca meiadiferenca_2 (.a(v), .b(meiadiferenca_1_s0), .s0(s0), .s1(meiadiferenca_2_s1));
  or or_1 (s1, meiadiferenca_2_s1, meiadiferenca_1_s1);
endmodule
