// Logisim project guia04_02.circ as structural Verilog: 2 circuits, main circuit meia soma
module meia_soma (
  input  a,
  input  b,
  output s0,
  output s1
);

  xor xor_1 (s0, a, b);
  and and_1 (s1, b, a);

  // Notes on the sheet:
  //   Circuito Meia Soma - Anderson
endmodule

module somacompleta (
  input  v,
  input  a,
  input  b,
  output s0,
  output s1
);

  wire meia_soma_1_s0, meia_soma_1_s1, meia_soma_2_s1;

  meia_soma meia_soma_1 (.a(a), .b(b), .s0(meia_soma_1_s0), .s1(meia_soma_1_s1));
  meia_soma meia_soma_2 (.a(v), .b(meia_soma_1_s0), .s0(s0), .s1(meia_soma_2_s1));
  or or_1 (s1, meia_soma_2_s1, meia_soma_1_s1);
endmodule
