// Logisim project Guia04_01.circ as structural Verilog: 1 circuit, main circuit main
module main (
  input  a,
  input  b,
  input  a_2,
  input  b_2,
  output s0,
  output s1,
  output s0_2,
  output s1_2
);

  wire NOR_2_out, NOR_3_out, NOR_4_out, NOR_5_out, NOR_6_out, NOR_out;

  nor NOR (NOR_out, a_2, a_2);
  nor NOR_2 (NOR_2_out, b_2, b_2);
  nor NOR_3 (NOR_3_out, b_2, a_2);
  nor NOR_4 (NOR_4_out, a_2, a_2);
  nor NOR_5 (NOR_5_out, b_2, b_2);
  xor xor_1 (s0, a, b);
  and and_1 (s1, a, b);
  nor NOR_6 (NOR_6_out, NOR_out, NOR_2_out);
  nor NOR_7 (s0_2, NOR_6_out, NOR_3_out);
  nor NOR_8 (s1_2, NOR_4_out, NOR_5_out);

  // Notes on the sheet:
  //   Half-Adder para Comparaçao de Resultado
  //   Guia04_01 - Bruno Cezar Andrade Viallet - 396679
  //   5 NOR = 1 XOR
  //   3 NOR = 1 AND
endmodule
