// Logisim project Guia04_02.circ as structural Verilog: 2 circuits, main circuit halfadder
module halfadder (
  input  a,
  input  b,
  output s0,
  output s1
);

  xor xor_1 (s0, a, b);
  and and_1 (s1, a, b);

  // Notes on the sheet:
  //   Half Adder
endmodule

module fulladder (
  input  c,
  input  a,
  input  b,
  output s0,
  output s1
);

  wire halfadder_1_s1, halfadder_2_s0, halfadder_2_s1;

  halfadder halfadder_1 (.a(c), .b(halfadder_2_s0), .s0(s0), .s1(halfadder_1_s1));
  halfadder halfadder_2 (.a(a), .b(b), .s0(halfadder_2_s0), .s1(halfadder_2_s1));
  or or_1 (s1, halfadder_1_s1, halfadder_2_s1);

  // Notes on the sheet:
  //   Guia04_02 - Bruno Cezar Andrade Viallet - 396679
endmodule
