// Logisim project Guia04_03.circ as structural Verilog: 2 circuits, main circuit halfsubtractor
module halfsubtractor (
  input  a,
  input  b,
  output s0,
  output s1
);

  wire not_1_out;

  not not_1 (not_1_out, a);
  xor xor_1 (s0, a, b);
  and and_1 (s1, b, not_1_out);
endmodule

module fullsubtractor (
  input  c,
  input  a,
  input  b,
  output s0,
  output s1
);

  wire halfsubtractor_1_s0, halfsubtractor_1_s1, halfsubtractor_2_s1;

  halfsubtractor halfsubtractor_1 (.a(a), .b(b), .s0(halfsubtractor_1_s0), .s1(halfsubtractor_1_s1));
  halfsubtractor halfsubtractor_2 (.a(c), .b(halfsubtractor_1_s0), .s0(s0), .s1(halfsubtractor_2_s1));
  or or_1 (s1, halfsubtractor_2_s1, halfsubtractor_1_s1);
endmodule
