// Logisim project G04_01.circ as structural Verilog: 1 circuit, main circuit main
module main (
  input  A,
  input  B,
  output S0,
  output S1
);

  wire B_E_NA_out, N_A_E_B_out, N_B_E_NA_out, N_NB_E_A_out, NB_E_A_out, \NÃO_A_out , \NÃO_B_out ;

  nand \NÃO_A  (\NÃO_A_out , A, A);
  nand N_A_E_B (N_A_E_B_out, A, B);
  nand \NÃO_B  (\NÃO_B_out , B, B);
  nand A_E_B (S1, N_A_E_B_out, N_A_E_B_out);
  nand N_NB_E_A (N_NB_E_A_out, \NÃO_B_out , A);
  nand N_B_E_NA (N_B_E_NA_out, \NÃO_A_out , B);
  nand NB_E_A (NB_E_A_out, N_NB_E_A_out, N_NB_E_A_out);
  nand B_E_NA (B_E_NA_out, N_B_E_NA_out, N_B_E_NA_out);
  or or_1 (S0, NB_E_A_out, B_E_NA_out);
endmodule
