// Logisim project G04_03.circ as structural Verilog: 2 circuits, main circuit main
module main (
  input  A,
  input  B,
  output S0,
  output out_4
);

  wire B_E_NA_out, N_A_E_B_out, N_B_E_NA_out, N_NB_E_A_out, NB_E_A_out, \NÃO_A_out , \NÃO_B_out ;

  nand \NÃO_A  (\NÃO_A_out , A, A);
  nand N_A_E_B (N_A_E_B_out, \NÃO_A_out , B);
  nand \NÃO_B  (\NÃO_B_out , B, B);
  nand A_E_B (out_4, N_A_E_B_out, N_A_E_B_out);
  nand N_NB_E_A (N_NB_E_A_out, \NÃO_B_out , A);
  nand N_B_E_NA (N_B_E_NA_out, \NÃO_A_out , B);
  nand NB_E_A (NB_E_A_out, N_NB_E_A_out, N_NB_E_A_out);
  nand B_E_NA (B_E_NA_out, N_B_E_NA_out, N_B_E_NA_out);
  or or_1 (S0, NB_E_A_out, B_E_NA_out);
endmodule

module \DIFERENÇA_COMPLETA  (
  input  A,
  input  B,
  input  C
);

  wire main_1_out_4, main_1_s0, main_2_out_4, main_2_s0, xor_1_out;

  main main_1 (.A(A), .B(B), .S0(main_1_s0), .out_4(main_1_out_4));
  main main_2 (.A(main_1_s0), .B(C), .S0(main_2_s0), .out_4(main_2_out_4));
  xor xor_1 (xor_1_out, main_2_out_4, main_1_out_4);
endmodule
