// Logisim project diferencacompleta.circ as structural Verilog: 2 circuits, main circuit main
module main (
  input  e1,
  input  x,
  input  y,
  input  e1_2,
  input  x_2,
  input  y_2,
  output s0,
  output s1,
  output s0_2,
  output s1_2
);

  wire a_out, halfdifference_1_s0, halfdifference_1_s1, halfdifference_2_s1, not_1_out, not_2_out, s_out,
       v2_out;

  xor s (s_out, x, y);
  not not_1 (not_1_out, x);
  halfdifference halfdifference_1 (.x(x_2), .y(y_2), .s0(halfdifference_1_s0), .s1(halfdifference_1_s1));
  and a (a_out, not_1_out, y);
  halfdifference halfdifference_2 (.x(e1_2), .y(halfdifference_1_s0), .s0(s0_2), .s1(halfdifference_2_s1));
  not not_2 (not_2_out, s_out);
  xor u_s0 (s0, e1, s_out);
  and v2 (v2_out, e1, not_2_out);
  or u_s1 (s1_2, halfdifference_2_s1, halfdifference_1_s1);
  or u_s1_2 (s1, v2_out, a_out);

  // Notes on the sheet:
  //   Diferenca-completa
  //   Guia 04 - capitulo 3
  //   Nome: Karen Alves Pereira    Matricula: 407451
endmodule

module halfdifference (
  input  x,
  input  y,
  output s0,
  output s1
);

  wire not_1_out;

  xor s (s0, x, y);
  not not_1 (not_1_out, x);
  and a (s1, not_1_out, y);
endmodule
