// Logisim project meiasomanor.circ as structural Verilog: 1 circuit, main circuit main
module main (
  input  a,
  input  b,
  output v1,
  output s
);

  wire tem1_out, tem2_out, tem3_out, tem4_out, tem5_out;

  nor tem1 (tem1_out, a, a);
  nor tem2 (tem2_out, b, b);
  nor tem3 (tem3_out, a, b);
  nor u_v1 (v1, tem1_out, tem2_out);
  nor tem4 (tem4_out, tem3_out, tem3_out);
  nor tem5 (tem5_out, tem4_out, tem4_out);
  nor u_s (s, v1, tem5_out);

  // Notes on the sheet:
  //   Guia 04 - Capitulo 3  
  //   Nome: Karen Alves Pereira  Matricula:407451
  //   Meia-soma com portas NOR
endmodule
