// Logisim project somacompleta.circ as structural Verilog: 2 circuits, main circuit main
module main (
  input  v1,
  input  x,
  input  y,
  input  v1_2,
  input  x_2,
  input  y_2,
  output s0,
  output s2,
  output s0_2,
  output s2_2
);

  wire a_out, halfadder_1_s, halfadder_1_s1, halfadder_2_s1, s_out, v2_out;

  halfadder halfadder_1 (.x(x_2), .y(y_2), .s(halfadder_1_s), .s1(halfadder_1_s1));
  xor s (s_out, x, y);
  and a (a_out, x, y);
  halfadder halfadder_2 (.x(v1_2), .y(halfadder_1_s), .s(s0_2), .s1(halfadder_2_s1));
  xor u_s0 (s0, v1, s_out);
  and v2 (v2_out, v1, s_out);
  or u_s2 (s2_2, halfadder_2_s1, halfadder_1_s1);
  or u_s2_2 (s2, v2_out, a_out);

  // Notes on the sheet:
  //   Nome: Karen Alves Pereida
  //   Guia 04 - Capitulo 3
  //   Soma-Completa
  //   Matricula: 407451
endmodule

module halfadder (
  input  x,
  input  y,
  output s,
  output s1
);

  xor u_s (s, x, y);
  and a (s1, x, y);

  // Notes on the sheet:
  //   Nome: Karen Alves Pereira / Matricula: 407451
  //   Meia-soma
endmodule
