// Logisim project Guia0402.circ as structural Verilog: 2 circuits, main circuit main
module main (
  input  a,
  input  b,
  input  c,
  output s,
  output c_2
);

  wire meiasoma_1_c, meiasoma_1_s, meiasoma_2_c;

  MeiaSoma meiasoma_1 (.a(a), .b(b), .s(meiasoma_1_s), .c(meiasoma_1_c));
  MeiaSoma meiasoma_2 (.a(meiasoma_1_s), .b(c), .s(s), .c(meiasoma_2_c));
  or or_1 (c_2, meiasoma_2_c, meiasoma_1_c);
endmodule

module MeiaSoma (
  input  a,
  input  b,
  output s,
  output c
);

  xor xor_1 (s, a, b);
  and and_1 (c, a, b);
endmodule
