// Logisim project Guia0403.circ as structural Verilog: 2 circuits, main circuit main
module main (
  input  a,
  input  b,
  input  c,
  output s,
  output c_2
);

  wire meiadiferenca_1_c, meiadiferenca_1_s, meiadiferenca_2_c;

  MeiaDiferenca meiadiferenca_1 (.a(a), .b(b), .s(meiadiferenca_1_s), .c(meiadiferenca_1_c));
  MeiaDiferenca meiadiferenca_2 (.a(meiadiferenca_1_s), .b(c), .s(s), .c(meiadiferenca_2_c));
  or or_1 (c_2, meiadiferenca_2_c, meiadiferenca_1_c);

  // Notes on the sheet:
  //   a-b
  //   (a-b) - c
endmodule

module MeiaDiferenca (
  input  a,
  input  b,
  output s,
  output c
);

  wire not_1_out;

  not not_1 (not_1_out, a);
  xor xor_1 (s, a, b);
  and and_1 (c, not_1_out, b);

  // Notes on the sheet:
  //   a-b
endmodule
