// Logisim project Guia0404.circ as structural Verilog: 1 circuit, main circuit main
module main (
  input  a,
  input  b,
  output out_3,
  output c
);

  wire nand_1_out, nand_2_out, nand_3_out, nand_4_out, nand_5_out;

  not nand_1 (nand_1_out, a);  // NAND_Gate
  not nand_2 (nand_2_out, b);  // NAND_Gate
  nand nand_3 (nand_3_out, nand_1_out, b);
  nand nand_4 (nand_4_out, a, nand_2_out);
  nand nand_5 (nand_5_out, nand_1_out, b);
  not nand_6 (c, nand_3_out);  // NAND_Gate
  nand nand_7 (out_3, nand_4_out, nand_5_out);
endmodule
