// Logisim project Guia0405.circ as structural Verilog
module MD (
  input  a,
  input  b,
  output s,
  output c
);

  wire nor_1_out, nor_2_out, nor_3_out, nor_4_out, nor_5_out, nor_6_out;

  not nor_1 (nor_1_out, a);  // NOR_Gate
  not nor_2 (nor_2_out, b);  // NOR_Gate
  not nor_3 (nor_3_out, nor_1_out);  // NOR_Gate
  nor nor_4 (nor_4_out, a, nor_2_out);
  nor nor_5 (nor_5_out, nor_1_out, b);
  nor nor_6 (nor_6_out, nor_4_out, nor_5_out);
  not nor_7 (s, nor_6_out);  // NOR_Gate
  nor nor_8 (c, nor_3_out, nor_2_out);
endmodule
