// Logisim project Guia04.circ as structural Verilog: 5 circuits, main circuit Exercicio01
module Exercicio01 (
  input  a,
  input  b,
  output Soma,
  output Carry
);

  wire nand_1_out, nand_2_out, nand_3_out, nand_5_out, nand_6_out, nand_7_out;

  nand nand_1 (nand_1_out, b, a);
  nand nand_2 (nand_2_out, a, a);
  nand nand_3 (nand_3_out, b, b);
  nand nand_4 (Carry, nand_1_out, nand_1_out);
  nand nand_5 (nand_5_out, nand_2_out, nand_3_out);
  nand nand_6 (nand_6_out, Carry, Carry);
  nand nand_7 (nand_7_out, nand_5_out, nand_6_out);
  nand nand_8 (Soma, nand_7_out, nand_7_out);

  // Notes on the sheet:
  //   Larissa Fernandes Leijoto - 410476
endmodule

module Exercicio02 (
  input  a,
  input  b,
  input  c,
  output Soma,
  output Carryout
);

  wire and_1_out, and_2_out, xor_1_out;

  xor xor_1 (xor_1_out, a, b);
  and and_1 (and_1_out, a, b);
  xor xor_2 (Soma, xor_1_out, c);
  and and_2 (and_2_out, xor_1_out, c);
  or or_1 (Carryout, and_1_out, and_2_out);
endmodule

module Exercicio03 (
  input  a,
  input  b,
  input  c,
  output \Diferença ,
  output Sinal
);

  wire \exercicio04_1_diferença , exercicio04_1_sinal, exercicio04_2_sinal;

  Exercicio04 exercicio04_1 (.a(a), .b(b), .\Diferença (\exercicio04_1_diferença ), .Sinal(exercicio04_1_sinal));
  Exercicio04 exercicio04_2 (
    .a(c), .b(\exercicio04_1_diferença ), .\Diferença (\Diferença ), .Sinal(exercicio04_2_sinal));
  or or_1 (Sinal, exercicio04_2_sinal, exercicio04_1_sinal);

  // Notes on the sheet:
  //   Meia Diferença 
endmodule

module Exercicio04 (
  input  a,
  input  b,
  output \Diferença ,
  output Sinal
);

  wire nor_1_out, nor_2_out, nor_3_out, nor_4_out, nor_5_out, nor_6_out, nor_7_out;

  nor nor_1 (nor_1_out, a, a);
  nor nor_2 (nor_2_out, a, a);
  nor nor_3 (nor_3_out, b, b);
  nor nor_4 (nor_4_out, a, b);
  nor nor_5 (nor_5_out, b, b);
  nor nor_6 (nor_6_out, nor_1_out, nor_1_out);
  nor nor_7 (nor_7_out, nor_2_out, nor_3_out);
  nor nor_8 (\Diferença , nor_7_out, nor_4_out);
  nor nor_9 (Sinal, nor_5_out, nor_6_out);
endmodule

module Exercicio05 (
  input  a,
  input  b,
  input  c,
  output \diferença ,
  output sinal
);

  wire \exercicio04_1_diferença , exercicio04_1_sinal, exercicio04_2_sinal;

  Exercicio04 exercicio04_1 (.a(a), .b(b), .\Diferença (\exercicio04_1_diferença ), .Sinal(exercicio04_1_sinal));
  Exercicio04 exercicio04_2 (
    .a(\exercicio04_1_diferença ), .b(c), .\Diferença (\diferença ), .Sinal(exercicio04_2_sinal));
  or or_1 (sinal, exercicio04_2_sinal, exercicio04_1_sinal);
endmodule
