// Logisim project halfadder.circ as structural Verilog: 1 circuit, main circuit main
module main (
  input  p,
  input  q,
  output s0,
  output s1
);

  wire nand_1_out, nand_2_out, nand_3_out, nand_4_out, nand_5_out, nand_7_out, nand_8_out, nand_9_out;

  nand nand_1 (nand_1_out, q, q);
  nand nand_2 (nand_2_out, p, p);
  nand nand_3 (nand_3_out, q, p);
  nand nand_4 (nand_4_out, q, p);
  nand nand_5 (nand_5_out, nand_1_out, nand_2_out);
  nand nand_6 (s1, nand_3_out, nand_4_out);
  nand nand_7 (nand_7_out, s1, s1);
  nand nand_8 (nand_8_out, nand_5_out, nand_7_out);
  nand nand_9 (nand_9_out, nand_7_out, nand_5_out);
  nand nand_10 (s0, nand_8_out, nand_9_out);

  // Notes on the sheet:
  //   OR
  //   temp1
  //   temp2
  //   temp4
  //   temp5
  //   AND
  //   HALF ADDER - NAND
  //   s1
  //   NOT
  //   temp3
  //   temp6
  //   AND
  //   temp7
  //   temp8
endmodule
