// Logisim project Half_adder.circ as structural Verilog: 2 circuits, main circuit main
module main (
  input  p,
  input  q,
  output s0,
  output s1
);

  xor xor_1 (s0, p, q);
  and and_1 (s1, q, p);
endmodule

module Soma_completa (
  input  vai_um,
  input  p,
  input  q,
  output s0,
  output s1
);

  wire main_1_s0, main_1_s1, main_2_s1;

  main main_1 (.p(p), .q(q), .s0(main_1_s0), .s1(main_1_s1));
  main main_2 (.p(vai_um), .q(main_1_s0), .s0(s0), .s1(main_2_s1));
  or or_1 (s1, main_2_s1, main_1_s1);

  // Notes on the sheet:
  //   temp1
  //   temp2
  //   temp3
endmodule
