// Logisim project Diferenca_completa.circ as structural Verilog: 2 circuits, main circuit meia_diferenca
module meia_diferenca (
  input  p,
  input  q,
  output s0,
  output s1
);

  wire not_1_out;

  not not_1 (not_1_out, p);
  xor xor_1 (s0, p, q);
  and and_1 (s1, q, not_1_out);
endmodule

module diferenca_completa (
  input  vem_um,
  input  x,
  input  y,
  input  p,
  input  q,
  output s0,
  output s1,
  output s0_2,
  output s1_2
);

  wire meia_diferenca_1_s0, meia_diferenca_1_s1, meia_diferenca_2_s1, not_1_out;

  meia_diferenca meia_diferenca_1 (.p(x), .q(y), .s0(meia_diferenca_1_s0), .s1(meia_diferenca_1_s1));
  not not_1 (not_1_out, p);
  meia_diferenca meia_diferenca_2 (.p(meia_diferenca_1_s0), .q(vem_um), .s0(s0), .s1(meia_diferenca_2_s1));
  xor xor_1 (s0_2, p, q);
  and and_1 (s1_2, q, not_1_out);
  or or_1 (s1, meia_diferenca_2_s1, meia_diferenca_1_s1);

  // Notes on the sheet:
  //   temp1
  //   temp2
endmodule
