// Logisim project Exerc04.circ as structural Verilog: 1 circuit, main circuit main
module main (
  input  p,
  input  q,
  output s0,
  output s1
);

  wire nor_1_out, nor_2_out, nor_3_out, nor_4_out, nor_5_out, nor_6_out, nor_7_out;

  nor nor_1 (nor_1_out, p, p);
  nor nor_2 (nor_2_out, q, q);
  nor nor_3 (nor_3_out, q, p);
  nor nor_4 (nor_4_out, p, p);
  nor nor_5 (nor_5_out, nor_1_out, nor_2_out);
  nor nor_6 (nor_6_out, q, q);
  nor nor_7 (nor_7_out, nor_4_out, nor_4_out);
  nor nor_8 (s0, nor_5_out, nor_3_out);
  nor nor_9 (s1, nor_6_out, nor_7_out);

  // Notes on the sheet:
  //   temp5
  //   temp6
  //   temp8
  //   temp1
  //   temp7
  //   temp3
  //   temp2
endmodule
