// Logisim project Excer05.circ as structural Verilog: 2 circuits, main circuit main
module main (
  input  p,
  input  q,
  output d,
  output v
);

  wire nand_1_out, nand_2_out, nand_3_out, nand_4_out, nand_5_out, nand_6_out;

  nand nand_1 (nand_1_out, q, p);
  nand nand_2 (nand_2_out, p, p);
  nand nand_3 (nand_3_out, q, nand_1_out);
  nand nand_4 (nand_4_out, nand_1_out, p);
  nand nand_5 (nand_5_out, q, nand_2_out);
  nand nand_6 (nand_6_out, nand_2_out, q);
  nand nand_7 (d, nand_3_out, nand_4_out);
  nand nand_8 (v, nand_5_out, nand_6_out);

  // Notes on the sheet:
  //   Xor
  //   q
  //   p
  //   Not
  //   q
  //   temp4
  //   p
  //   q
  //   temp1
  //   q
  //   temp5
  //   temp6
  //   temp2
  //   temp3
  //   And
endmodule

module \Diferença_Completa  (
  input  x,
  input  y,
  input  vem_um,
  output s1,
  output s0
);

  wire main_1_d, main_1_v, main_2_v, nand_1_out, nand_2_out;

  main main_1 (.p(x), .q(y), .d(main_1_d), .v(main_1_v));
  main main_2 (.p(main_1_d), .q(vem_um), .d(s0), .v(main_2_v));
  nand nand_1 (nand_1_out, main_2_v, main_2_v);
  nand nand_2 (nand_2_out, main_1_v, main_1_v);
  nand nand_3 (s1, nand_1_out, nand_2_out);

  // Notes on the sheet:
  //   s0
  //   temp3
  //   temp1
  //   temp2
  //   And
endmodule
