// Logisim project circuito01.circ as structural Verilog: 1 circuit, main circuit main
module main (
  input  a,
  input  b,
  output s1,
  output s2
);

  wire s3_out, s4_out, s5_out, s6_out, s7_out;

  nor s3 (s3_out, a, a);
  nor s4 (s4_out, b, b);
  nor s5 (s5_out, a, b);
  nor nor_1 (s1, s3_out, s4_out);
  nor s6 (s6_out, s5_out, s5_out);
  nor nor_2 (s2, s1, s7_out);
  nor s7 (s7_out, s6_out, s6_out);

  // Notes on the sheet:
  //   Paulo Henrique de Almeida Amorim
  //   Circuito Hald Adder
endmodule
