// Logisim project circuito02.circ as structural Verilog: 2 circuits, main circuit main
module main (
  input  s1,
  input  a,
  input  b,
  output s2,
  output s3
);

  wire halfadder_1_out_4, halfadder_2_out_3, halfadder_2_out_4;

  halfadder halfadder_1 (.in_1(s1), .in_2(halfadder_2_out_3), .out_3(s2), .out_4(halfadder_1_out_4));
  halfadder halfadder_2 (.in_1(a), .in_2(b), .out_3(halfadder_2_out_3), .out_4(halfadder_2_out_4));
  or or_1 (s3, halfadder_1_out_4, halfadder_2_out_4);

  // Notes on the sheet:
  //   Paulo Henrique de Almeida Amorim
  //   half1
  //   half2
  //   Circuito Full Adder
endmodule

module halfadder (
  input  in_1,
  input  in_2,
  output out_3,
  output out_4
);

  xor xor_1 (out_3, in_1, in_2);
  and and_1 (out_4, in_1, in_2);
endmodule
