// Logisim project circuito03.circ as structural Verilog: 3 circuits, main circuit main
module main (
  input  s1,
  input  a,
  input  b,
  output s2,
  output s3
);

  wire halfdiference2_1_out_4, halfdiference_1_out_3, halfdiference_1_out_4;

  halfdiference halfdiference_1 (.in_1(a), .in_2(b), .out_3(halfdiference_1_out_3), .out_4(halfdiference_1_out_4));
  halfdiference2 halfdiference2_1 (.in_1(s1), .in_2(halfdiference_1_out_3), .out_3(s2), .out_4(halfdiference2_1_out_4));
  or or_1 (s3, halfdiference2_1_out_4, halfdiference_1_out_4);

  // Notes on the sheet:
  //   Paulo Henrique de Almeida Amorim
  //   halfdiference
  //   halfdiference2
  //   Circuito Full Difference
endmodule

module halfdiference (
  input  in_1,
  input  in_2,
  output out_3,
  output out_4
);

  wire not_1_out;

  xor xor_1 (out_3, in_1, in_2);
  not not_1 (not_1_out, in_1);
  and and_1 (out_4, not_1_out, in_2);
endmodule

module halfdiference2 (
  input  in_1,
  input  in_2,
  output out_3,
  output out_4
);

  wire not_1_out;

  not not_1 (not_1_out, in_2);
  and and_1 (out_4, in_1, not_1_out);
  xor xor_1 (out_3, in_1, in_2);
endmodule
