// Logisim project Simulaçoes Guia 04.circ as structural Verilog: 8 circuits, main circuit meia-soma
module meia_somaNAND (
  input  a,
  input  b,
  output s0,
  output s1
);

  wire temp1_out, temp2_out, temp3_out, temp4_out;

  nand temp1 (temp1_out, a, b);
  nand temp4 (temp4_out, b, a);
  nand temp2 (temp2_out, a, temp1_out);
  nand temp3 (temp3_out, temp1_out, b);
  nand temp5 (s0, temp4_out, temp4_out);
  nand temp4_2 (s1, temp2_out, temp3_out);

  // Notes on the sheet:
  //   Silvino Henrique Santos de Souza - 412773
  //   Circuito Meia - Soma usando Somente NANDs
  //   temp5 = s0
  //   temp 4 = s1
endmodule

module meia_soma (
  input  a,
  input  b,
  output s0,
  output s1
);

  and and_1 (s0, b, a);
  xor xor_1 (s1, a, b);

  // Notes on the sheet:
  //   Silvino Henrique Santos de Souza - 412773
  //   Meia -Soma Compacto
endmodule

module somador_completo (
  input  a,
  input  b,
  input  Cin,
  output Cout,
  output Soma
);

  wire meia_soma_1_s0, meia_soma_1_s1, meia_soma_2_s0;

  or or_1 (Cout, meia_soma_1_s0, meia_soma_2_s0);
  meia_soma meia_soma_1 (.a(a), .b(b), .s0(meia_soma_1_s0), .s1(meia_soma_1_s1));
  meia_soma meia_soma_2 (.a(meia_soma_1_s1), .b(Cin), .s0(meia_soma_2_s0), .s1(Soma));

  // Notes on the sheet:
  //   Silvino Henrique Santos de Souza - 412773
  //   Somador Completo 
endmodule

module \meia_diferença  (
  input  a,
  input  b,
  output s0,
  output s1
);

  wire not_1_out;

  and and_1 (s0, b, not_1_out);
  not not_1 (not_1_out, a);
  xor xor_1 (s1, a, b);

  // Notes on the sheet:
  //   Silvino Henrique Santos de Souza - 412773
  //   Meia - Diferença Compacto
endmodule

module \meia_diferençaNOR  (
  input  a,
  input  b,
  output s0,
  output s1
);

  wire nor_1_out, nor_2_out, nor_3_out, nor_4_out, nor_5_out, nor_6_out, nor_7_out;

  nor nor_1 (nor_1_out, a, a);
  nor nor_2 (nor_2_out, a, b);
  nor nor_3 (nor_3_out, a, nor_2_out);
  nor nor_4 (nor_4_out, nor_2_out, b);
  nor nor_5 (nor_5_out, nor_1_out, nor_1_out);
  nor nor_6 (nor_6_out, b, b);
  nor nor_7 (nor_7_out, nor_3_out, nor_4_out);
  nor nor_8 (s0, nor_5_out, nor_6_out);
  not nor_9 (s1, nor_7_out);  // NOR_Gate

  // Notes on the sheet:
  //   Silvino Henrique Santos de Souza - 412773
  //   Meia-Diferença somente com NORs
endmodule

module subtrator_completo (
  input  a,
  input  b,
  input  Cin,
  output Cout,
  output \Diferença 
);

  wire \meia_diferença_1_s0 , \meia_diferença_1_s1 , \meia_diferença_2_s0 ;

  or or_1 (Cout, \meia_diferença_1_s0 , \meia_diferença_2_s0 );
  \meia_diferença  \meia_diferença_1  (.a(a), .b(b), .s0(\meia_diferença_1_s0 ), .s1(\meia_diferença_1_s1 ));
  \meia_diferença  \meia_diferença_2  (
    .a(\meia_diferença_1_s1 ), .b(Cin), .s0(\meia_diferença_2_s0 ), .s1(\Diferença ));

  // Notes on the sheet:
  //   Cin: pull=down
  //   Silvino Henrique Santos de Souza - 412773
  //   Subtrator Completo 
endmodule

module \meia_diferençaNAND  (
  input  a,
  input  b,
  output s0,
  output s1
);

  wire nand_1_out, temp1_out, temp2_out, temp3_out, temp4_out;

  nand nand_1 (nand_1_out, a, a);
  nand temp1 (temp1_out, a, b);
  nand temp4 (temp4_out, b, nand_1_out);
  nand temp2 (temp2_out, a, temp1_out);
  nand temp3 (temp3_out, temp1_out, b);
  nand temp5 (s0, temp4_out, temp4_out);
  nand temp4_2 (s1, temp2_out, temp3_out);

  // Notes on the sheet:
  //   Silvino Henrique Santos de Souza - 412773
  //   Circuito Meia - Diferença usando Somente NANDs
  //   temp 4 = s1
endmodule

module Subtrator_completo2 (
  input  a,
  input  b,
  input  Cin,
  output Cout,
  output \Diferença 
);

  wire \meia_diferençanand_1_s0 , \meia_diferençanand_2_s0 , \meia_diferençanand_2_s1 ;

  or or_1 (Cout, \meia_diferençanand_2_s0 , \meia_diferençanand_1_s0 );
  \meia_diferençaNAND  \meia_diferençanand_1  (
    .a(\meia_diferençanand_2_s1 ), .b(Cin), .s0(\meia_diferençanand_1_s0 ), .s1(\Diferença ));
  \meia_diferençaNAND  \meia_diferençanand_2  (
    .a(a), .b(b), .s0(\meia_diferençanand_2_s0 ), .s1(\meia_diferençanand_2_s1 ));

  // Notes on the sheet:
  //   Cin: pull=down
  //   Silvino Henrique Santos de Souza - 412773
  //   Subtrator Completo (subcircuito com NANDs)
endmodule
