// Logisim project guia04_03.circ as structural Verilog: 2 circuits, main circuit meiadiferenca
module meiadiferenca (
  input  a,
  input  b,
  output s0,
  output s1
);

  wire not_1_out;

  not not_1 (not_1_out, a);
  xor xor_1 (s0, a, b);
  and and_1 (s1, b, not_1_out);

  // Notes on the sheet:
  //   Meia Diferença - Anderson
endmodule

module diferencacompleta (
  input  v,
  input  a,
  input  b,
  output s0,
  output s1
);

  wire meiadiferenca_1_s0, meiadiferenca_1_s1, meiadiferenca_2_s1;

  meiadiferenca meiadiferenca_1 (.a(a), .b(b), .s0(meiadiferenca_1_s0), .s1(meiadiferenca_1_s1));
  meiadiferenca meiadiferenca_2 (.a(v), .b(meiadiferenca_1_s0), .s0(s0), .s1(meiadiferenca_2_s1));
  or or_1 (s1, meiadiferenca_2_s1, meiadiferenca_1_s1);
endmodule
