// Logisim project guia04_05.circ as structural Verilog: 2 circuits, main circuit meiadiferenca
module meiadiferenca (
  input  a,
  input  b,
  output s0,
  output s1
);

  wire nand_2_out, nand_3_out, nand_4_out, nand_5_out, nand_6_out;

  // NAND_Gate nand_1 has open pins: in1=a, in3=b, out=open
  nand nand_2 (nand_2_out, a, a);
  nand nand_3 (nand_3_out, a, b);
  nand nand_4 (nand_4_out, b, nand_2_out);
  nand nand_5 (nand_5_out, a, nand_3_out);
  nand nand_6 (nand_6_out, nand_3_out, b);
  nand nand_7 (s1, nand_4_out, nand_4_out);
  nand nand_8 (s0, nand_5_out, nand_6_out);

  // Notes on the sheet:
  //   Meia diferenca NAND- Anderson
  //   s2
  //   s6
  //   s3
  //   s7
  //   s1
  //   s4
  //   s5
endmodule

module diferencacompleta (
  input  v,
  input  a,
  input  b,
  output s0,
  output s1
);

  wire meiadiferenca_1_s0, meiadiferenca_1_s1, meiadiferenca_2_s1;

  meiadiferenca meiadiferenca_1 (.a(a), .b(b), .s0(meiadiferenca_1_s0), .s1(meiadiferenca_1_s1));
  meiadiferenca meiadiferenca_2 (.a(v), .b(meiadiferenca_1_s0), .s0(s0), .s1(meiadiferenca_2_s1));
  or or_1 (s1, meiadiferenca_2_s1, meiadiferenca_1_s1);
endmodule
