// Logisim project Exercicio 02.circ as structural Verilog: 3 circuits, main circuit HalfAdder
module HalfAdder (
  input  A,
  input  B,
  output S,
  output Cout
);

  xor xor_1 (S, A, B);
  and and_1 (Cout, A, B);

  // Notes on the sheet:
  //   Bruno César Lopes Silva - 415985
endmodule

module FullAdder (
  input  A,
  input  B,
  input  Carry_In,
  output S,
  output s1
);

  wire halfadder_1_cout, halfadder_1_s, halfadder_2_cout;

  HalfAdder halfadder_1 (.A(A), .B(B), .S(halfadder_1_s), .Cout(halfadder_1_cout));
  HalfAdder halfadder_2 (.A(halfadder_1_s), .B(Carry_In), .S(S), .Cout(halfadder_2_cout));
  or or_1 (s1, halfadder_2_cout, halfadder_1_cout);

  // Notes on the sheet:
  //   Bruno César Lopes Silva - 415985
endmodule

module FullAdder2 (
  input  A,
  input  B,
  input  Carry_In,
  output S,
  output s1
);

  FullAdder fulladder_1 (.A(A), .B(B), .Carry_In(Carry_In), .S(S), .s1(s1));

  // Notes on the sheet:
  //   Bruno César Lopes Silva - 415985
endmodule
