// Logisim project Exercicio 03.circ as structural Verilog: 3 circuits, main circuit HalfSubtractor
module HalfSubtractor (
  input  A,
  input  B,
  output S,
  output s1
);

  wire not_1_out;

  not not_1 (not_1_out, A);
  xor xor_1 (S, A, B);
  and and_1 (s1, not_1_out, B);

  // Notes on the sheet:
  //   Bruno César Lopes Silva - 415985
endmodule

module FullSubtractor (
  input  A,
  input  B,
  input  Vem_Um,
  output S,
  output s1
);

  wire halfsubtractor_1_s, halfsubtractor_1_s1, halfsubtractor_2_s1;

  HalfSubtractor halfsubtractor_1 (.A(A), .B(B), .S(halfsubtractor_1_s), .s1(halfsubtractor_1_s1));
  HalfSubtractor halfsubtractor_2 (.A(halfsubtractor_1_s), .B(Vem_Um), .S(S), .s1(halfsubtractor_2_s1));
  or or_1 (s1, halfsubtractor_2_s1, halfsubtractor_1_s1);

  // Notes on the sheet:
  //   Bruno César Lopes Silva - 415985 
endmodule

module FullSubtractor2 (
  input  A,
  input  B,
  input  Vem_um,
  output S,
  output s1
);

  FullSubtractor fullsubtractor_1 (.A(A), .B(B), .Vem_Um(Vem_um), .S(S), .s1(s1));

  // Notes on the sheet:
  //   Bruno César Lopes Silva - 415985
endmodule
