// Logisim project Exercicio 04.circ as structural Verilog: 1 circuit, main circuit HalfSubtractor_Nor
module HalfSubtractor_Nor (
  input  A,
  input  B,
  output S,
  output s1
);

  wire nor_1_out, nor_2_out, nor_3_out, nor_5_out;

  nor nor_1 (nor_1_out, A, A);
  nor nor_2 (nor_2_out, B, B);
  nor nor_3 (nor_3_out, nor_1_out, B);
  nor nor_4 (s1, nor_2_out, A);
  nor nor_5 (nor_5_out, nor_3_out, s1);
  nor nor_6 (S, nor_5_out, nor_5_out);

  // Notes on the sheet:
  //   Bruno César Lopes Silva - 415985
endmodule
