// Logisim project Exercicio 05.circ as structural Verilog: 3 circuits, main circuit HalfSubtractor_Nand
module HalfSubtractor_Nand (
  input  A,
  input  B,
  output S,
  output s1
);

  wire nand_1_out, nand_2_out, nand_3_out, nand_4_out;

  nand nand_1 (nand_1_out, A, A);
  nand nand_2 (nand_2_out, B, B);
  nand nand_3 (nand_3_out, nand_1_out, B);
  nand nand_4 (nand_4_out, A, nand_2_out);
  nand nand_5 (S, nand_3_out, nand_4_out);
  nand nand_6 (s1, nand_3_out, nand_3_out);

  // Notes on the sheet:
  //   Bruno César Lopes Silva - 415985
endmodule

module FullSubtractor_Nand (
  input  A,
  input  B,
  input  Vem_Um,
  output S,
  output s1
);

  wire halfsubtractor_nand_1_s, halfsubtractor_nand_1_s1, halfsubtractor_nand_2_s1, nand_1_out, nand_2_out;

  HalfSubtractor_Nand halfsubtractor_nand_1 (.A(A), .B(B), .S(halfsubtractor_nand_1_s), .s1(halfsubtractor_nand_1_s1));
  HalfSubtractor_Nand halfsubtractor_nand_2 (
    .A(halfsubtractor_nand_1_s), .B(Vem_Um), .S(S), .s1(halfsubtractor_nand_2_s1));
  nand nand_1 (nand_1_out, halfsubtractor_nand_1_s1, halfsubtractor_nand_1_s1);
  nand nand_2 (nand_2_out, halfsubtractor_nand_2_s1, halfsubtractor_nand_2_s1);
  nand nand_3 (s1, nand_1_out, nand_2_out);

  // Notes on the sheet:
  //   Bruno César Lopes Silva - 415985
endmodule

module FullSubtractor_Nand2 (
  input  A,
  input  B,
  input  Vem_Um,
  output S,
  output s1
);

  FullSubtractor_Nand fullsubtractor_nand_1 (.A(A), .B(B), .Vem_Um(Vem_Um), .S(S), .s1(s1));

  // Notes on the sheet:
  //   Bruno César Lopes Silva - 415985
endmodule
