// Logisim project Guia_04.circ as structural Verilog: 4 circuits, main circuit Half Adder
module Half_Adder (
  input  A,
  input  B,
  output s1,
  output s0
);

  wire nor_1_out, nor_2_out, nor_3_out, nor_4_out, nor_5_out, nor_6_out, nor_8_out;

  nor nor_1 (nor_1_out, A, A);
  nor nor_2 (nor_2_out, B, B);
  nor nor_3 (nor_3_out, A, A);
  nor nor_4 (nor_4_out, B, B);
  nor nor_5 (nor_5_out, nor_3_out, B);
  nor nor_6 (nor_6_out, nor_4_out, A);
  nor nor_7 (s1, nor_1_out, nor_2_out);
  nor nor_8 (nor_8_out, nor_5_out, nor_6_out);
  nor nor_9 (s0, nor_8_out, nor_8_out);

  // Notes on the sheet:
  //   Aluno: Alyson Deives
  //   Matricula: 416589
  //   Guia 04_01 - Half Adder with NOR gates
endmodule

module Full_Adder (
  input  A,
  input  B,
  input  C,
  output s1,
  output s0
);

  wire half_adder_1_s0, half_adder_1_s1, half_adder_2_s1;

  Half_Adder half_adder_1 (.A(B), .B(A), .s1(half_adder_1_s1), .s0(half_adder_1_s0));
  Half_Adder half_adder_2 (.A(C), .B(half_adder_1_s0), .s1(half_adder_2_s1), .s0(s0));
  or or_1 (s1, half_adder_1_s1, half_adder_2_s1);

  // Notes on the sheet:
  //   Aluno: Alyson Deives
  //   Matricula: 416589
  //   Guia 04_02 - Full Adder with NOR gates
endmodule

module Half_Differ (
  input  A,
  input  B,
  output s1,
  output s0
);

  wire nor_1_out, nor_2_out, nor_3_out, nor_4_out, nor_5_out, nor_7_out;

  nor nor_1 (nor_1_out, B, B);
  nor nor_2 (nor_2_out, A, A);
  nor nor_3 (nor_3_out, B, B);
  nor nor_4 (nor_4_out, nor_2_out, B);
  nor nor_5 (nor_5_out, nor_3_out, A);
  nor nor_6 (s1, A, nor_1_out);
  nor nor_7 (nor_7_out, nor_4_out, nor_5_out);
  nor nor_8 (s0, nor_7_out, nor_7_out);

  // Notes on the sheet:
  //   Aluno: Alyson Deives
  //   Matricula: 416589
  //   Guia 03_05 - Half Differ with NOR gates
endmodule

module Full_Differ (
  input  A,
  input  B,
  input  C,
  output s1,
  output s0
);

  wire half_differ_1_s0, half_differ_1_s1, half_differ_2_s0;

  Half_Differ half_differ_1 (.A(A), .B(B), .s1(half_differ_1_s1), .s0(half_differ_1_s0));
  Half_Differ half_differ_2 (.A(half_differ_1_s0), .B(C), .s1(s1), .s0(half_differ_2_s0));
  or or_1 (s0, half_differ_1_s1, half_differ_2_s0);

  // Notes on the sheet:
  //   Aluno: Alyson Deives
  //   Matricula: 416589
  //   Guia 04_03 - Half Differ with NOR gates
endmodule
