// Logisim project guia04-01.circ as structural Verilog: 1 circuit, main circuit main
module main (
  input  x,
  input  y,
  output s,
  output Vout
);

  wire nor_1_out, nor_2_out, nor_3_out, nor_4_out, nor_5_out, nor_6_out;

  nor nor_1 (nor_1_out, x, x);
  nor nor_2 (nor_2_out, y, y);
  nor nor_3 (nor_3_out, y, x);
  nor nor_4 (nor_4_out, y, y);
  nor nor_5 (nor_5_out, x, x);
  nor nor_6 (nor_6_out, nor_1_out, nor_2_out);
  nor nor_7 (Vout, nor_4_out, nor_5_out);
  nor nor_8 (s, nor_6_out, nor_3_out);

  // Notes on the sheet:
  //   Meia soma com nor
  //   xor
  //   and
endmodule
