// Logisim project guia04-02.circ as structural Verilog: 2 circuits, main circuit main
module main (
  input  x,
  input  y,
  output s,
  output Vout
);

  xor xor_1 (s, x, y);
  and and_1 (Vout, y, x);

  // Notes on the sheet:
  //   Meia soma compacta
endmodule

module SC (
  input  Vin,
  input  x,
  input  y,
  output s,
  output Vout
);

  wire main_1_vout, main_2_s, main_2_vout;

  main main_1 (.x(Vin), .y(main_2_s), .s(s), .Vout(main_1_vout));
  main main_2 (.x(x), .y(y), .s(main_2_s), .Vout(main_2_vout));
  or or_1 (Vout, main_1_vout, main_2_vout);

  // Notes on the sheet:
  //   Soma completa com subcircuitos
endmodule
