// Logisim project guia04-03.circ as structural Verilog: 2 circuits, main circuit main
module main (
  input  x,
  input  y,
  output d,
  output Vout
);

  wire not_1_out;

  not not_1 (not_1_out, x);
  xor xor_1 (d, x, y);
  and and_1 (Vout, not_1_out, y);

  // Notes on the sheet:
  //   Meia diferença compacta
endmodule

module DC (
  input  Vin,
  input  x,
  input  y,
  output d,
  output Vout
);

  wire main_1_d, main_1_vout, main_2_vout;

  main main_1 (.x(x), .y(y), .d(main_1_d), .Vout(main_1_vout));
  main main_2 (.x(main_1_d), .y(Vin), .d(d), .Vout(main_2_vout));
  or or_1 (Vout, main_2_vout, main_1_vout);

  // Notes on the sheet:
  //   Meia diferença com subcircuitos
endmodule
