// Logisim project guia04-04.circ as structural Verilog: 1 circuit, main circuit main
module main (
  input  x,
  input  y,
  output d,
  output Vout
);

  wire nor_1_out, nor_2_out, nor_3_out, nor_4_out, nor_5_out, nor_6_out, nor_7_out;

  nor nor_1 (nor_1_out, x, x);
  nor nor_2 (nor_2_out, x, x);
  nor nor_3 (nor_3_out, y, y);
  nor nor_4 (nor_4_out, y, x);
  nor nor_5 (nor_5_out, nor_2_out, nor_3_out);
  nor nor_6 (nor_6_out, y, y);
  nor nor_7 (nor_7_out, nor_1_out, nor_1_out);
  nor nor_8 (d, nor_5_out, nor_4_out);
  nor nor_9 (Vout, nor_6_out, nor_7_out);

  // Notes on the sheet:
  //   Meia diferença nors
  //   not
  //   xor
  //   and
endmodule
