// Logisim project guia04-05.circ as structural Verilog: 1 circuit, main circuit main
module main (
  input  Vin,
  input  x,
  input  y,
  output d,
  output Vout
);

  wire nand_1_out, nand_2_out, nand_3_out, nand_4_out, nand_5_out, nand_6_out, nand_7_out, nand_8_out,
       nand_9_out, nand_10_out, nand_11_out, nand_12_out, nand_14_out, nand_15_out, nand_16_out;

  nand nand_1 (nand_1_out, x, x);
  nand nand_2 (nand_2_out, x, y);
  nand nand_3 (nand_3_out, y, nand_1_out);
  nand nand_4 (nand_4_out, x, nand_2_out);
  nand nand_5 (nand_5_out, nand_2_out, y);
  nand nand_6 (nand_6_out, nand_3_out, nand_3_out);
  nand nand_7 (nand_7_out, nand_4_out, nand_5_out);
  nand nand_8 (nand_8_out, Vin, nand_7_out);
  nand nand_9 (nand_9_out, nand_7_out, nand_7_out);
  nand nand_10 (nand_10_out, Vin, nand_8_out);
  nand nand_11 (nand_11_out, nand_8_out, nand_7_out);
  nand nand_12 (nand_12_out, Vin, nand_9_out);
  nand nand_13 (d, nand_10_out, nand_11_out);
  nand nand_14 (nand_14_out, nand_12_out, nand_12_out);
  nand nand_15 (nand_15_out, nand_14_out, nand_14_out);
  nand nand_16 (nand_16_out, nand_6_out, nand_6_out);
  nand nand_17 (Vout, nand_15_out, nand_16_out);

  // Notes on the sheet:
  //   not
  //   Diferença completa com nands
  //   xor
  //   and
  //   not
  //   xor
  //   and
  //   or
endmodule
