// Logisim project guia4_2Logisim.circ as structural Verilog: 2 circuits, main circuit main
module main (
  input  x,
  input  y,
  output out_3,
  output out_4
);

  xor xor_1 (out_3, x, y);
  and and_1 (out_4, y, x);
endmodule

module soma_completa (
  input  Vin,
  input  X,
  input  Y,
  output out_4,
  output out_5
);

  wire main_1_out_3, main_1_out_4, main_2_out_4;

  main main_1 (.x(X), .y(Y), .out_3(main_1_out_3), .out_4(main_1_out_4));
  main main_2 (.x(Vin), .y(main_1_out_3), .out_3(out_4), .out_4(main_2_out_4));
  xor xor_1 (out_5, main_2_out_4, main_1_out_4);
endmodule
