// Logisim project guia4_3Logisim.circ as structural Verilog: 2 circuits, main circuit main
module main (
  input  X,
  input  Y,
  output D,
  output Vout
);

  wire not_1_out;

  not not_1 (not_1_out, X);
  xor xor_1 (D, X, Y);
  and and_1 (Vout, not_1_out, Y);

  // Notes on the sheet:
  //   Meia Diferença
endmodule

module diferenca_completa (
  input  Vin,
  input  X,
  input  Y,
  output D,
  output Vout
);

  wire main_1_d, main_1_vout, main_2_vout;

  main main_1 (.X(X), .Y(Y), .D(main_1_d), .Vout(main_1_vout));
  main main_2 (.X(main_1_d), .Y(Vin), .D(D), .Vout(main_2_vout));
  or or_1 (Vout, main_2_vout, main_1_vout);
endmodule
