// Logisim project Guia04.circ as structural Verilog: 6 circuits, main circuit Ex02 - Full Adder
module Ex01___Half_Adder_Standard_Nand (
  input  a,
  input  b,
  output Soma,
  output Cout
);

  wire nand_1_out, nand_2_out, nand_3_out, nand_4_out, nand_5_out;

  nand nand_1 (nand_1_out, a, a);
  nand nand_2 (nand_2_out, b, b);
  nand nand_3 (nand_3_out, b, a);
  nand nand_4 (nand_4_out, nand_1_out, nand_2_out);
  nand nand_5 (nand_5_out, nand_4_out, nand_3_out);
  nand nand_6 (Cout, nand_3_out, nand_3_out);
  nand nand_7 (Soma, nand_5_out, nand_5_out);

  // Notes on the sheet:
  //   Douglas de Loredo Borges - 417889
endmodule

module Ex02___Full_Adder (
  input  a,
  input  b,
  input  Cin,
  output Soma,
  output Cout
);

  wire ex01_half_adder_standard_nand_1_cout, ex01_half_adder_standard_nand_1_soma,
       ex01_half_adder_standard_nand_2_cout;

  Ex01___Half_Adder_Standard_Nand ex01_half_adder_standard_nand_1 (
    .a(a), .b(b), .Soma(ex01_half_adder_standard_nand_1_soma), .Cout(ex01_half_adder_standard_nand_1_cout));
  Ex01___Half_Adder_Standard_Nand ex01_half_adder_standard_nand_2 (
    .a(ex01_half_adder_standard_nand_1_soma), .b(Cin), .Soma(Soma),
    .Cout(ex01_half_adder_standard_nand_2_cout));
  or or_1 (Cout, ex01_half_adder_standard_nand_2_cout, ex01_half_adder_standard_nand_1_cout);
endmodule

module Ex03___Full_Subtractor (
  input  a,
  input  b,
  input  Vin,
  output \Diferença ,
  output Vout
);

  wire \ex04_half_subtractor_compact_nor_1_diferença , ex04_half_subtractor_compact_nor_1_vout,
       ex04_half_subtractor_compact_nor_2_vout;

  Ex04___Half_Subtractor_Compact_Nor ex04_half_subtractor_compact_nor_1 (
    .a(a), .b(b), .\Diferença (\ex04_half_subtractor_compact_nor_1_diferença ),
    .Vout(ex04_half_subtractor_compact_nor_1_vout));
  Ex04___Half_Subtractor_Compact_Nor ex04_half_subtractor_compact_nor_2 (
    .a(\ex04_half_subtractor_compact_nor_1_diferença ), .b(Vin), .\Diferença (\Diferença ),
    .Vout(ex04_half_subtractor_compact_nor_2_vout));
  or or_1 (Vout, ex04_half_subtractor_compact_nor_2_vout, ex04_half_subtractor_compact_nor_1_vout);
endmodule

module Ex04___Half_Subtractor_Compact_Nor (
  input  a,
  input  b,
  output \Diferença ,
  output Vout
);

  wire nor_1_out, nor_2_out, nor_3_out, nor_4_out, nor_5_out;

  nor nor_1 (nor_1_out, a, a);
  nor nor_2 (nor_2_out, nor_1_out, nor_3_out);
  nor nor_3 (nor_3_out, b, b);
  nor nor_4 (nor_4_out, a, b);
  nor nor_5 (nor_5_out, b, b);
  nor nor_6 (Vout, nor_5_out, a);
  nor nor_7 (\Diferença , nor_2_out, nor_4_out);

  // Notes on the sheet:
  //   Douglas de Loredo Borges - 417889
endmodule

module Half_Subtractor_Compact_Nand (
  input  a,
  input  b,
  output \Subtração ,
  output Vin
);

  wire nand_1_out, nand_2_out, nand_3_out, nand_4_out, nand_5_out;

  nand nand_1 (nand_1_out, a, b);
  nand nand_2 (nand_2_out, a, a);
  nand nand_3 (nand_3_out, a, nand_1_out);
  nand nand_4 (nand_4_out, nand_1_out, b);
  nand nand_5 (nand_5_out, b, nand_2_out);
  nand nand_6 (\Subtração , nand_3_out, nand_4_out);
  nand nand_7 (Vin, nand_5_out, nand_5_out);

  // Notes on the sheet:
  //   Douglas de Loredo Borges - 417889
endmodule

module Ex05___Full_Subtractor (
  input  a,
  input  b,
  input  Vin,
  output \Diferença ,
  output Vout
);

  wire \half_subtractor_compact_nand_1_subtração , half_subtractor_compact_nand_1_vin,
       half_subtractor_compact_nand_2_vin;

  Half_Subtractor_Compact_Nand half_subtractor_compact_nand_1 (
    .a(a), .b(b), .\Subtração (\half_subtractor_compact_nand_1_subtração ),
    .Vin(half_subtractor_compact_nand_1_vin));
  Half_Subtractor_Compact_Nand half_subtractor_compact_nand_2 (
    .a(\half_subtractor_compact_nand_1_subtração ), .b(Vin), .\Subtração (\Diferença ),
    .Vin(half_subtractor_compact_nand_2_vin));
  or or_1 (Vout, half_subtractor_compact_nand_2_vin, half_subtractor_compact_nand_1_vin);
endmodule
