// Logisim project Circuitos 1 a 5.circ as structural Verilog: 6 circuits, main circuit Exercicio01
module Exercicio01 (
  input  e1,
  input  e2,
  output soma,
  output carry
);

  wire nand_1_out, nand_2_out, nand_3_out, nand_4_out, nand_5_out;

  nand nand_1 (nand_1_out, e1, e1);
  nand nand_2 (nand_2_out, e2, e2);
  nand nand_3 (nand_3_out, e2, e1);
  nand nand_4 (nand_4_out, nand_1_out, nand_2_out);
  nand nand_5 (nand_5_out, nand_4_out, nand_3_out, nand_3_out);
  nand nand_6 (carry, nand_3_out, nand_3_out);
  nand nand_7 (soma, nand_5_out, nand_5_out);

  // Notes on the sheet:
  //   Isabella Gonçales - 420120
endmodule

module Exercicio02 (
  input  e1,
  input  e2,
  input  carryin,
  output carry,
  output soma
);

  wire exercicio01_1_carry, exercicio01_1_soma, exercicio01_2_carry;

  Exercicio01 exercicio01_1 (.e1(e1), .e2(e2), .soma(exercicio01_1_soma), .carry(exercicio01_1_carry));
  Exercicio01 exercicio01_2 (.e1(carryin), .e2(exercicio01_1_soma), .soma(soma), .carry(exercicio01_2_carry));
  or or_1 (carry, exercicio01_1_carry, exercicio01_2_carry);

  // Notes on the sheet:
  //   Isabella Gonçales - 420120
endmodule

module Exercicio03 (
  input  e1,
  input  e2,
  input  vin,
  output \diferença ,
  output sinal
);

  wire \exercicio04_1_diferença , exercicio04_1_sinal, exercicio04_2_sinal;

  Exercicio04 exercicio04_1 (.e1(e1), .e2(e2), .\diferença (\exercicio04_1_diferença ), .sinal(exercicio04_1_sinal));
  Exercicio04 exercicio04_2 (
    .e1(\exercicio04_1_diferença ), .e2(vin), .\diferença (\diferença ), .sinal(exercicio04_2_sinal));
  or or_1 (sinal, exercicio04_1_sinal, exercicio04_2_sinal);

  // Notes on the sheet:
  //   Isabella Gonçales - 420120
endmodule

module Exercicio04 (
  input  e1,
  input  e2,
  output \diferença ,
  output sinal
);

  wire nor_1_out, nor_2_out, nor_3_out, nor_4_out, nor_5_out;

  nor nor_1 (nor_1_out, e1, e1);
  nor nor_2 (nor_2_out, e2, e2);
  nor nor_3 (nor_3_out, e1, e2);
  nor nor_4 (nor_4_out, e2, e2);
  nor nor_5 (nor_5_out, nor_1_out, nor_2_out);
  nor nor_6 (sinal, nor_4_out, e1);
  nor nor_7 (\diferença , nor_5_out, nor_3_out);

  // Notes on the sheet:
  //   Isabella Gonçales - 420120
endmodule

module Exercicio05 (
  input  e1,
  input  e2,
  input  vin,
  output diferenca,
  output sinal
);

  wire \meia_diferença_nand_1_diferença , \meia_diferença_nand_1_sinal , \meia_diferença_nand_2_sinal ;

  \Meia_Diferença_Nand  \meia_diferença_nand_1  (
    .e1(e2), .e2(e1), .\diferença (\meia_diferença_nand_1_diferença ), .sinal(\meia_diferença_nand_1_sinal ));
  \Meia_Diferença_Nand  \meia_diferença_nand_2  (
    .e1(\meia_diferença_nand_1_diferença ), .e2(vin), .\diferença (diferenca),
    .sinal(\meia_diferença_nand_2_sinal ));
  or or_1 (sinal, \meia_diferença_nand_1_sinal , \meia_diferença_nand_2_sinal );

  // Notes on the sheet:
  //   Isabella Gonçales - 420120
endmodule

module \Meia_Diferença_Nand  (
  input  e1,
  input  e2,
  output \diferença ,
  output sinal
);

  wire nand_1_out, nand_2_out, nand_3_out, nand_4_out, nand_6_out;

  nand nand_1 (nand_1_out, e1, e2);
  nand nand_2 (nand_2_out, e1, nand_1_out, nand_1_out);
  nand nand_3 (nand_3_out, nand_1_out, e2);
  nand nand_4 (nand_4_out, e1, e1, e1);
  nand nand_5 (\diferença , nand_2_out, nand_3_out);
  nand nand_6 (nand_6_out, e2, nand_4_out);
  nand nand_7 (sinal, nand_6_out, nand_6_out);
endmodule
