// Logisim project Exemplo02.circ as structural Verilog: 2 circuits, main circuit main
module main (
  input  in_1,
  input  in_2,
  input  in_3,
  output out_4,
  output out_5
);

  wire meiasoma_1_out_3, meiasoma_1_out_4, meiasoma_2_out_4;

  meiaSoma meiasoma_1 (.in_1(in_2), .in_2(in_3), .out_3(meiasoma_1_out_3), .out_4(meiasoma_1_out_4));
  meiaSoma meiasoma_2 (.in_1(in_1), .in_2(meiasoma_1_out_3), .out_3(out_4), .out_4(meiasoma_2_out_4));
  or or_1 (out_5, meiasoma_2_out_4, meiasoma_1_out_4);
endmodule

module meiaSoma (
  input  in_1,
  input  in_2,
  output out_3,
  output out_4
);

  wire nand_1_out, nand_2_out, nand_3_out, nand_4_out;

  nand nand_1 (nand_1_out, in_1, in_2);
  nand nand_2 (nand_2_out, in_1, in_2);
  nand nand_3 (nand_3_out, in_1, in_1, nand_1_out);
  nand nand_4 (nand_4_out, nand_1_out, in_2);
  nand nand_5 (out_4, nand_2_out, nand_2_out);
  nand nand_6 (out_3, nand_3_out, nand_4_out);
endmodule
