// Logisim project cir..circ as structural Verilog: 3 circuits, main circuit exercicio02
module exercicio02 (
  input  a,
  input  b,
  input  vai_um,
  output s0,
  output s1
);

  wire _1_out, _2_2_out, _2_out;

  xor _2 (_2_out, a, b);
  and _2_2 (_2_2_out, a, b);
  and _1 (_1_out, _2_out, vai_um);
  xor _1_2 (s0, vai_um, _2_out);
  or _1_3 (s1, _1_out, _2_2_out);

  // Notes on the sheet:
  //   Operador Soma Completa - Modelo Compacto
  //   s4
  //   s5
  //   s3
  //   s2
endmodule

module exercicio01 (
  input  a,
  input  b,
  output s0,
  output s1
);

  wire _1_out, _2_out, _3_out, _4_out, _6_out;

  nand _4 (_4_out, a, b);
  nand _1 (_1_out, a, a);
  nand _2 (_2_out, b, b);
  nand _5 (s1, _4_out, _4_out);
  nand _3 (_3_out, _1_out, _2_out);
  nand _6 (_6_out, _3_out, _4_out);
  nand _7 (s0, _6_out, _6_out);

  // Notes on the sheet:
  //   s4
  //   AND1
  //   Operador Meia Soma - Modelo Tradicional
  //   OR1
  //   s5
  //   s6
  //   s3
  //   AND2
  //   s2
endmodule

module exercicio03 (
  input  a,
  input  b,
  input  in_3,
  output s0,
  output s1
);

  wire _1_2_out, _1_3_out, _1_out, _2_3_out, _2_out;

  not _1 (_1_out, a);
  xor _1_2 (_1_2_out, a, b);
  and _1_3 (_1_3_out, b, _1_out);
  not _2 (_2_out, _1_2_out);
  nor _2_2 (s0, in_3, _1_2_out);
  and _2_3 (_2_3_out, in_3, _2_out);
  or _1_4 (s1, _2_3_out, _1_3_out);

  // Notes on the sheet:
  //   Operador Difereça Completa - Modelo Compacto
endmodule
