// Logisim project Exercicio01.circ as structural Verilog: 1 circuit, main circuit main
module main (
  input  a,
  input  b
);

  // NOR_Gate nor_1 is placed but not wired
  // NOR_Gate nor_2 is placed but not wired
  // NOR_Gate nor_3 is placed but not wired
  // NOR_Gate nor_4 is placed but not wired
  // NOR_Gate nor_5 is placed but not wired
  // NOR_Gate nor_6 is placed but not wired
  // NOR_Gate nor_7 is placed but not wired
  // NOR_Gate nor_8 is placed but not wired

  // Notes on the sheet:
  //   v1
  //   s
endmodule
