// Logisim project guia04_04.circ as structural Verilog: 1 circuit, main circuit main
module main (
  input  a,
  input  b,
  output out_3,
  output out_4
);

  wire s2_out, s3_out, s4_out, s5_out, s6_out;

  nor s2 (s2_out, a, a);
  nor s3 (s3_out, b, b);
  nor s6 (s6_out, s2_out, s2_out);
  nor s4 (s4_out, s2_out, s3_out);
  nor s5 (s5_out, b, a);
  nor s1 (out_3, s6_out, s3_out);
  nor s0 (out_4, s4_out, s5_out);

  // Notes on the sheet:
  //   Gabriel Benjamim de Carvalho
endmodule
