// Logisim project Ex1.circ as structural Verilog: 1 circuit, main circuit main
module main (
  input  in_1,
  input  in_2,
  input  p,
  input  q,
  output out_5,
  output out_6,
  output s1,
  output s0
);

  wire _1_out, _2_out, _3_out, _4_out, _6_out, _7_out, not_1_out, or_1_out;

  or or_1 (or_1_out, in_2, in_1);
  and and_1 (out_6, in_2, in_1);
  not not_1 (not_1_out, out_6);
  nand _1 (_1_out, p, p);
  nand _2 (_2_out, p, q);
  nand _3 (_3_out, q, q);
  and and_2 (out_5, or_1_out, not_1_out);
  nand _4 (_4_out, _1_out, _3_out);
  nand _5 (s0, _2_out, _2_out);
  nand _6 (_6_out, s0, s0);
  nand _7 (_7_out, _4_out, _6_out);
  nand _8 (s1, _7_out, _7_out);
endmodule
