// Logisim project Ex1_2010.circ as structural Verilog: 1 circuit, main circuit main
module main (
  input  in_1,
  input  in_2,
  input  P,
  input  Q,
  output out_5,
  output out_6,
  output _5,
  output S1
);

  wire nor_1_out, nor_2_out, nor_3_out, not_1_out, or_1_out;

  or or_1 (or_1_out, in_2, in_1);
  and and_1 (out_6, in_2, in_1);
  not not_1 (not_1_out, out_6);
  nor nor_1 (nor_1_out, P, Q);
  nor nor_2 (nor_2_out, P, P);
  nor nor_3 (nor_3_out, Q, Q);
  and and_2 (out_5, or_1_out, not_1_out);
  nor nor_4 (S1, nor_2_out, nor_3_out);
  nor nor_5 (_5, nor_1_out, S1);

  // Notes on the sheet:
  //   1
  //   2
  //   3
  //   s2
  //   s3
  //   4
  //   s4
  //   s5
  //   S0
endmodule
