// Logisim project Ex2.circ as structural Verilog: 2 circuits, main circuit main
module main (
  input  e1,
  input  e2,
  input  e3,
  output s0,
  output s1
);

  wire ha_1_s0, ha_1_s1, ha_2_s1;

  HA ha_1 (.a(e2), .b(e3), .s0(ha_1_s0), .s1(ha_1_s1));
  HA ha_2 (.a(e1), .b(ha_1_s0), .s0(s0), .s1(ha_2_s1));
  or or_1 (s1, ha_2_s1, ha_1_s1);

  // Notes on the sheet:
  //   2
  //   1
endmodule

module HA (
  input  a,
  input  b,
  output s0,
  output s1
);

  xor xor_1 (s0, a, b);
  and and_1 (s1, a, b);
endmodule
