// Logisim project Ex3.circ as structural Verilog: 2 circuits, main circuit main
module main (
  input  e1,
  input  e2,
  input  e3,
  output s0,
  output s1
);

  wire hs_1_s0, hs_1_s1, hs_2_s1;

  HS hs_1 (.e1(e1), .e2(e2), .s0(hs_1_s0), .s1(hs_1_s1));
  HS hs_2 (.e1(hs_1_s0), .e2(e3), .s0(s0), .s1(hs_2_s1));
  or or_1 (s1, hs_2_s1, hs_1_s1);

  // Notes on the sheet:
  //   1
  //   f1
  //   2
  //   f2
  //   f3
endmodule

module HS (
  input  e1,
  input  e2,
  output s0,
  output s1
);

  wire not_1_out;

  not not_1 (not_1_out, e1);
  xor xor_1 (s0, e1, e2);
  and and_1 (s1, e2, not_1_out);

  // Notes on the sheet:
  //   q
endmodule
