// Logisim project diferencacompleto.circ as structural Verilog: 1 circuit, main circuit main
module main (
  input  a,
  input  b,
  input  v,
  output s0,
  output s1
);

  wire and_1_out, and_2_out, and_3_out, xor_1_out;

  xor xor_1 (xor_1_out, b, v);
  and and_1 (and_1_out, a, xor_1_out);
  and and_2 (and_2_out, b, v);
  and and_3 (and_3_out, xor_1_out, a);
  or or_1 (s1, and_2_out, and_3_out);
  or or_2 (s0, a, and_1_out);
endmodule
