// Logisim project somadorcompleto.circ as structural Verilog: 1 circuit, main circuit main
module main (
  input  a,
  input  b,
  input  c,
  input  v,
  output s0,
  output s1
);

  wire and_1_out, and_2_out, and_3_out, and_4_out, and_5_out, and_6_out, and_7_out, and_8_out, not_1_out,
       or_1_out, xor_1_out, xor_2_out;

  xor xor_1 (xor_1_out, a, b);
  xor xor_2 (xor_2_out, v, c);
  and and_1 (and_1_out, a, b);
  and and_2 (and_2_out, c, v);
  and and_3 (and_3_out, b, a, v);
  and and_4 (and_4_out, xor_2_out, and_1_out);
  and and_5 (and_5_out, xor_2_out, b);
  not not_1 (not_1_out, b);
  or or_1 (or_1_out, v, and_3_out);
  and and_6 (and_6_out, not_1_out, a, xor_2_out);
  and and_7 (and_7_out, c, or_1_out);
  and and_8 (and_8_out, xor_1_out, and_2_out);
  or or_2 (s0, xor_1_out, and_4_out);
  or or_3 (s1, and_5_out, and_6_out, and_8_out, and_7_out);
endmodule
