// Logisim project Exercicio 01.circ as structural Verilog: 4 circuits, main circuit MeiaSoma
module MeiaSoma (
  input  a,
  input  b,
  output s,
  output s1
);

  xor xor_1 (s, a, b);
  and and_1 (s1, a, b);

  // Notes on the sheet:
  //   Bruno César Lopes Silva - 415985
endmodule

module SomaCompleta (
  input  a,
  input  b,
  input  vaium,
  output s,
  output s1
);

  wire meiasoma_1_s, meiasoma_1_s1, meiasoma_2_s1;

  MeiaSoma meiasoma_1 (.a(a), .b(b), .s(meiasoma_1_s), .s1(meiasoma_1_s1));
  MeiaSoma meiasoma_2 (.a(meiasoma_1_s), .b(vaium), .s(s), .s1(meiasoma_2_s1));
  or or_1 (s1, meiasoma_2_s1, meiasoma_1_s1);

  // Notes on the sheet:
  //   Bruno César Lopes Silva - 45985
endmodule

module Soma4Bits (
  input  b3,
  input  b2,
  input  b1,
  input  b0,
  input  a3,
  input  a2,
  input  a1,
  input  a0,
  output s4,
  output s3,
  output s2,
  output s1,
  output s0
);

  wire meiasoma_1_s1, somacompleta_2_s1, somacompleta_3_s1;

  SomaCompleta somacompleta_1 (.a(a3), .b(b3), .vaium(somacompleta_2_s1), .s(s3), .s1(s4));
  SomaCompleta somacompleta_2 (.a(a2), .b(b2), .vaium(somacompleta_3_s1), .s(s2), .s1(somacompleta_2_s1));
  SomaCompleta somacompleta_3 (.a(a1), .b(b1), .vaium(meiasoma_1_s1), .s(s1), .s1(somacompleta_3_s1));
  MeiaSoma meiasoma_1 (.a(a0), .b(b0), .s(s0), .s1(meiasoma_1_s1));

  // Notes on the sheet:
  //   Bruno César Lopes Silva - 415985
endmodule

module Soma4BitsFinal (
  input  [3:0] b,
  input  [3:0] a,
  output [4:0] s
);

  Soma4Bits soma4bits_1 (
    .b3(b[3]), .b2(b[2]), .b1(b[1]), .b0(b[0]), .a3(a[3]), .a2(a[2]), .a1(a[1]), .a0(a[0]), .s4(s[4]),
    .s3(s[3]), .s2(s[2]), .s1(s[1]), .s0(s[0]));

  // Notes on the sheet:
  //   Bruno César Lopes Silva - 415985
endmodule
