// Logisim project Exercicio 02.circ as structural Verilog: 4 circuits, main circuit HalfSubtractor
module HalfSubtractor (
  input  A,
  input  B,
  output S,
  output s1
);

  wire not_1_out;

  not not_1 (not_1_out, A);
  xor xor_1 (S, A, B);
  and and_1 (s1, not_1_out, B);

  // Notes on the sheet:
  //   Bruno César Lopes Silva - 415985
endmodule

module FullSubtractor (
  input  A,
  input  B,
  input  Vem_Um,
  output S,
  output s1
);

  wire halfsubtractor_1_s, halfsubtractor_1_s1, halfsubtractor_2_s1;

  HalfSubtractor halfsubtractor_1 (.A(A), .B(B), .S(halfsubtractor_1_s), .s1(halfsubtractor_1_s1));
  HalfSubtractor halfsubtractor_2 (.A(halfsubtractor_1_s), .B(Vem_Um), .S(S), .s1(halfsubtractor_2_s1));
  or or_1 (s1, halfsubtractor_2_s1, halfsubtractor_1_s1);

  // Notes on the sheet:
  //   Bruno César Lopes Silva - 415985 
endmodule

module DiferencaCompleta3Bits (
  input  b2,
  input  b1,
  input  b0,
  input  a2,
  input  a1,
  input  a0,
  output s3,
  output s2,
  output s1,
  output s0
);

  wire fullsubtractor_2_s1, halfsubtractor_1_s1;

  FullSubtractor fullsubtractor_1 (.A(a2), .B(b2), .Vem_Um(fullsubtractor_2_s1), .S(s2), .s1(s3));
  FullSubtractor fullsubtractor_2 (.A(a1), .B(b1), .Vem_Um(halfsubtractor_1_s1), .S(s1), .s1(fullsubtractor_2_s1));
  HalfSubtractor halfsubtractor_1 (.A(a0), .B(b0), .S(s0), .s1(halfsubtractor_1_s1));

  // Notes on the sheet:
  //   Bruno César Lopes Silva - 415985
endmodule

module DiferencaCompleta3BitsFinal (
  input  [2:0] b,
  input  [2:0] a,
  output [3:0] s
);

  DiferencaCompleta3Bits diferencacompleta3bits_1 (
    .b2(b[2]), .b1(b[1]), .b0(b[0]), .a2(a[2]), .a1(a[1]), .a0(a[0]), .s3(s[3]), .s2(s[2]), .s1(s[1]),
    .s0(s[0]));

  // Notes on the sheet:
  //   Bruno César Lopes Silva - 415985
endmodule
