// Logisim project Exercicio 04.circ as structural Verilog: 4 circuits, main circuit MeiaSomaNand
module MeiaSomaNand (
  input  a,
  input  b,
  output s,
  output s1
);

  wire nand_1_out, nand_2_out, nand_3_out, nand_4_out, nand_5_out;

  nand nand_1 (nand_1_out, a, a);
  nand nand_2 (nand_2_out, b, b);
  nand nand_3 (nand_3_out, a, b);
  nand nand_4 (nand_4_out, nand_1_out, b);
  nand nand_5 (nand_5_out, a, nand_2_out);
  nand nand_6 (s1, nand_3_out, nand_3_out);
  nand nand_7 (s, nand_4_out, nand_5_out);

  // Notes on the sheet:
  //   Bruno César Lopes Silva - 415985
endmodule

module SomaCompletaNand (
  input  a,
  input  b,
  input  vaium,
  output s,
  output s1
);

  wire meiasomanand_1_s, meiasomanand_1_s1, meiasomanand_2_s1, nand_1_out, nand_2_out;

  MeiaSomaNand meiasomanand_1 (.a(a), .b(b), .s(meiasomanand_1_s), .s1(meiasomanand_1_s1));
  nand nand_1 (nand_1_out, meiasomanand_1_s1, meiasomanand_1_s1);
  MeiaSomaNand meiasomanand_2 (.a(meiasomanand_1_s), .b(vaium), .s(s), .s1(meiasomanand_2_s1));
  nand nand_2 (nand_2_out, meiasomanand_2_s1, meiasomanand_2_s1);
  nand nand_3 (s1, nand_1_out, nand_2_out);

  // Notes on the sheet:
  //   Bruno César Lopes Silva - 415985
endmodule

module SomaNand3Bits (
  input  b2,
  input  b1,
  input  b0,
  input  a2,
  input  a1,
  input  a0,
  output s3,
  output s2,
  output s1,
  output s0
);

  wire meiasomanand_1_s1, somacompletanand_2_s1;

  SomaCompletaNand somacompletanand_1 (.a(a2), .b(b2), .vaium(somacompletanand_2_s1), .s(s2), .s1(s3));
  SomaCompletaNand somacompletanand_2 (.a(a1), .b(b1), .vaium(meiasomanand_1_s1), .s(s1), .s1(somacompletanand_2_s1));
  MeiaSomaNand meiasomanand_1 (.a(a0), .b(b0), .s(s0), .s1(meiasomanand_1_s1));

  // Notes on the sheet:
  //   Bruno César Lopes Silva - 415985
endmodule

module Soma3BitsFinal (
  input  [2:0] b,
  input  [2:0] a,
  output [3:0] s
);

  SomaNand3Bits somanand3bits_1 (
    .b2(b[2]), .b1(b[1]), .b0(b[0]), .a2(a[2]), .a1(a[1]), .a0(a[0]), .s3(s[3]), .s2(s[2]), .s1(s[1]),
    .s0(s[0]));

  // Notes on the sheet:
  //   Bruno César Lopes Silva - 415985
endmodule
