// Logisim project Exercicio 05.circ as structural Verilog: 4 circuits, main circuit MeiaDiferencaNor
module MeiaDiferencaNor (
  input  a,
  input  b,
  output s,
  output s1
);

  wire nor_1_out, nor_2_out, nor_3_out, nor_5_out;

  nor nor_1 (nor_1_out, a, a);
  nor nor_2 (nor_2_out, b, b);
  nor nor_3 (nor_3_out, nor_1_out, b);
  nor nor_4 (s1, a, nor_2_out);
  nor nor_5 (nor_5_out, nor_3_out, s1);
  nor nor_6 (s, nor_5_out, nor_5_out);

  // Notes on the sheet:
  //   Bruno César Lopes Silva - 415985
endmodule

module DiferencaCompletaNor (
  input  a,
  input  b,
  input  vemum,
  output s,
  output s1
);

  wire meiadiferencanor_1_s, meiadiferencanor_1_s1, meiadiferencanor_2_s1, nor_1_out;

  MeiaDiferencaNor meiadiferencanor_1 (.a(a), .b(b), .s(meiadiferencanor_1_s), .s1(meiadiferencanor_1_s1));
  MeiaDiferencaNor meiadiferencanor_2 (.a(meiadiferencanor_1_s), .b(vemum), .s(s), .s1(meiadiferencanor_2_s1));
  nor nor_1 (nor_1_out, meiadiferencanor_2_s1, meiadiferencanor_1_s1);
  nor nor_2 (s1, nor_1_out, nor_1_out);

  // Notes on the sheet:
  //   Bruno César Lopes Silva - 415985
endmodule

module Diferenca3Bits (
  input  b2,
  input  b1,
  input  b0,
  input  a2,
  input  a1,
  input  a0,
  output s3,
  output s2,
  output s1,
  output s0
);

  wire diferencacompletanor_2_s1, meiadiferencanor_1_s1;

  DiferencaCompletaNor diferencacompletanor_1 (.a(a2), .b(b2), .vemum(diferencacompletanor_2_s1), .s(s2), .s1(s3));
  DiferencaCompletaNor diferencacompletanor_2 (
    .a(a1), .b(b1), .vemum(meiadiferencanor_1_s1), .s(s1), .s1(diferencacompletanor_2_s1));
  MeiaDiferencaNor meiadiferencanor_1 (.a(a0), .b(b0), .s(s0), .s1(meiadiferencanor_1_s1));

  // Notes on the sheet:
  //   Bruno César Lopes Silva - 415985
endmodule

module Diferenca3BitsFinal (
  input  [2:0] b,
  input  [2:0] a,
  output [3:0] s
);

  Diferenca3Bits diferenca3bits_1 (
    .b2(b[2]), .b1(b[1]), .b0(b[0]), .a2(a[2]), .a1(a[1]), .a0(a[0]), .s3(s[3]), .s2(s[2]), .s1(s[1]),
    .s0(s[0]));

  // Notes on the sheet:
  //   Bruno César Lopes Silva - 415985
endmodule
