// Logisim project Exemplo 02.circ as structural Verilog: 3 circuits, main circuit circuito
module circuito (
  input  a0,
  input  b0,
  input  a1,
  input  b1,
  input  a2,
  input  b2,
  output s0,
  output s1,
  output s2,
  output s3
);

  wire subcircuitocomp_1_s1, subcircuitomeia_1_s1;

  subCircuitoMeia subcircuitomeia_1 (.a(a0), .b(b0), .s0(s0), .s1(subcircuitomeia_1_s1));
  subCircuitoComp subcircuitocomp_1 (.c(subcircuitomeia_1_s1), .a(a1), .b(b1), .s0(s1), .s1(subcircuitocomp_1_s1));
  subCircuitoComp subcircuitocomp_2 (.c(subcircuitocomp_1_s1), .a(a2), .b(b2), .s0(s2), .s1(s3));

  // Notes on the sheet:
  //   Nome: Bruno Rafael Nicolletti
endmodule

module subCircuitoMeia (
  input  a,
  input  b,
  output s0,
  output s1
);

  wire not_1_out;

  xor xor_1 (s0, a, b);
  not not_1 (not_1_out, a);
  and and_1 (s1, b, not_1_out);

  // Notes on the sheet:
  //   Nome: Bruno Rafael Nicolletti
endmodule

module subCircuitoComp (
  input  c,
  input  a,
  input  b,
  output s0,
  output s1
);

  wire subcircuitomeia_1_s0, subcircuitomeia_1_s1, subcircuitomeia_2_s1;

  subCircuitoMeia subcircuitomeia_1 (.a(a), .b(b), .s0(subcircuitomeia_1_s0), .s1(subcircuitomeia_1_s1));
  subCircuitoMeia subcircuitomeia_2 (.a(subcircuitomeia_1_s0), .b(c), .s0(s0), .s1(subcircuitomeia_2_s1));
  or or_1 (s1, subcircuitomeia_2_s1, subcircuitomeia_1_s1);

  // Notes on the sheet:
  //   Nome: Bruno Rafael Nicolletti
endmodule
