// Logisim project Exemplo 03.circ as structural Verilog: 3 circuits, main circuit circuito
module circuito (
  input  _0,
  input  a0,
  input  b0,
  input  a1,
  input  b1,
  output s0,
  output s1,
  output s2,
  output s3
);

  wire and_1_out, and_2_out, and_3_out, and_4_out, subcircuitocomp_1_s1, subcircuitomeia_2_s1;

  and and_1 (and_1_out, a1, b1);
  and and_2 (and_2_out, a0, b0);
  and and_3 (and_3_out, a0, b1);
  and and_4 (and_4_out, a1, b0);
  subCircuitoMeia subcircuitomeia_1 (.a(subcircuitocomp_1_s1), .b(and_1_out), .s0(s2), .s1(s3));
  subCircuitoMeia subcircuitomeia_2 (.a(_0), .b(and_2_out), .s0(s0), .s1(subcircuitomeia_2_s1));
  subCircuitoComp subcircuitocomp_1 (
    .c(subcircuitomeia_2_s1), .a(and_3_out), .b(and_4_out), .s0(s1), .s1(subcircuitocomp_1_s1));

  // Notes on the sheet:
  //   Nome: Bruno Rafael Nicolletti
endmodule

module subCircuitoMeia (
  input  a,
  input  b,
  output s0,
  output s1
);

  xor xor_1 (s0, a, b);
  and and_1 (s1, a, b);

  // Notes on the sheet:
  //   Nome: Bruno Rafael Nicolletti
endmodule

module subCircuitoComp (
  input  c,
  input  a,
  input  b,
  output s0,
  output s1
);

  wire subcircuitomeia_1_s0, subcircuitomeia_1_s1, subcircuitomeia_2_s1;

  subCircuitoMeia subcircuitomeia_1 (.a(a), .b(b), .s0(subcircuitomeia_1_s0), .s1(subcircuitomeia_1_s1));
  subCircuitoMeia subcircuitomeia_2 (.a(c), .b(subcircuitomeia_1_s0), .s0(s0), .s1(subcircuitomeia_2_s1));
  or or_1 (s1, subcircuitomeia_2_s1, subcircuitomeia_1_s1);

  // Notes on the sheet:
  //   Nome: Bruno Rafael Nicolletti
endmodule
