// Logisim project diferençacompleta.circ as structural Verilog
module HS (
  input  in_1,
  input  in_2,
  output out_3,
  output out_4
);

  wire not_1_out;

  not not_1 (not_1_out, in_1);
  xor xor_1 (out_3, in_1, in_2);
  and and_1 (out_4, in_2, not_1_out);

  // Notes on the sheet:
  //   q
endmodule

module FS_1bit (
  input  c,
  input  a,
  input  b,
  output s0,
  output s1
);

  wire hs_1_out_3, hs_1_out_4, hs_2_out_4;

  HS hs_1 (.in_1(a), .in_2(b), .out_3(hs_1_out_3), .out_4(hs_1_out_4));
  HS hs_2 (.in_1(hs_1_out_3), .in_2(c), .out_3(s0), .out_4(hs_2_out_4));
  or or_1 (s1, hs_2_out_4, hs_1_out_4);

  // Notes on the sheet:
  //   w1
  //   w2
  //   w3
endmodule

module FS_3bits (
  input  [2:0] a,
  input  [2:0] b,
  output [3:0] s
);

  wire fs_1bit_1_s1, hs_1_out_4;

  HS hs_1 (.in_1(a[0]), .in_2(b[0]), .out_3(s[0]), .out_4(hs_1_out_4));
  FS_1bit fs_1bit_1 (.c(hs_1_out_4), .a(a[1]), .b(b[1]), .s0(s[1]), .s1(fs_1bit_1_s1));
  FS_1bit fs_1bit_2 (.c(fs_1bit_1_s1), .a(a[2]), .b(b[2]), .s0(s[2]), .s1(s[3]));
endmodule
