// Logisim project produtocompleto.circ as structural Verilog
module HA (
  input  a,
  input  b,
  output s0,
  output s1
);

  xor xor_1 (s0, a, b);
  and and_1 (s1, a, b);
endmodule

module FA (
  input  vai_um,
  input  a,
  input  b,
  output s0,
  output s1
);

  wire ha_1_s0, ha_1_s1, ha_2_s1;

  HA ha_1 (.a(a), .b(b), .s0(ha_1_s0), .s1(ha_1_s1));
  HA ha_2 (.a(vai_um), .b(ha_1_s0), .s0(s0), .s1(ha_2_s1));
  or or_1 (s1, ha_2_s1, ha_1_s1);
endmodule

module Produto_3bits (
  input  [2:0] a,
  input  [2:0] b,
  output [5:0] s
);

  wire a0b1_out, a0b2_out, a1b0_out, a1b1_out, a1b2_out, a2b0_out, a2b1_out, a2b2_out, fa_1_s0, fa_1_s1,
       fa_2_s1, fa_3_s1, ha_1_s1;

  and a0b0 (s[0], a[0], b[0]);
  and a1b0 (a1b0_out, a[1], b[0]);
  and a0b1 (a0b1_out, a[0], b[1]);
  and a2b0 (a2b0_out, a[2], b[0]);
  and a1b1 (a1b1_out, a[1], b[1]);
  and a0b2 (a0b2_out, a[0], b[2]);
  and a2b1 (a2b1_out, a[2], b[1]);
  and a1b2 (a1b2_out, a[1], b[2]);
  and a2b2 (a2b2_out, a[2], b[2]);
  HA ha_1 (.a(a1b0_out), .b(a0b1_out), .s0(s[1]), .s1(ha_1_s1));
  FA fa_1 (.vai_um(ha_1_s1), .a(a2b0_out), .b(a1b1_out), .s0(fa_1_s0), .s1(fa_1_s1));
  FA fa_2 (.vai_um(fa_3_s1), .a(a2b1_out), .b(a1b2_out), .s0(s[3]), .s1(fa_2_s1));
  HA ha_2 (.a(fa_2_s1), .b(a2b2_out), .s0(s[4]), .s1(s[5]));
  FA fa_3 (.vai_um(fa_1_s0), .a(fa_1_s1), .b(a0b2_out), .s0(s[2]), .s1(fa_3_s1));
endmodule

module x (
  input  [2:0] a,
  input  [2:0] b,
  output [5:0] s
);

  wire a0b1_out, a0b2_out, a1b0_out, a1b1_out, a1b2_out, a2b0_out, a2b1_out, a2b2_out, fa_1_s1, fa_2_s1,
       fa_3_s0, fa_3_s1, ha_1_s1;

  and a0b0 (s[0], a[0], b[0]);
  and a1b0 (a1b0_out, a[1], b[0]);
  HA ha_1 (.a(a1b0_out), .b(a0b1_out), .s0(s[1]), .s1(ha_1_s1));
  and a0b1 (a0b1_out, a[0], b[1]);
  and a2b0 (a2b0_out, a[2], b[0]);
  and a1b1 (a1b1_out, a[1], b[1]);
  and a0b2 (a0b2_out, a[0], b[2]);
  FA fa_1 (.vai_um(fa_2_s1), .a(a2b1_out), .b(a1b2_out), .s0(s[3]), .s1(fa_1_s1));
  and a2b1 (a2b1_out, a[2], b[1]);
  and a1b2 (a1b2_out, a[1], b[2]);
  HA ha_2 (.a(fa_1_s1), .b(a2b2_out), .s0(s[4]), .s1(s[5]));
  and a2b2 (a2b2_out, a[2], b[2]);
  FA fa_2 (.vai_um(fa_3_s0), .a(fa_3_s1), .b(a0b2_out), .s0(s[2]), .s1(fa_2_s1));
  FA fa_3 (.vai_um(ha_1_s1), .a(a2b0_out), .b(a1b1_out), .s0(fa_3_s0), .s1(fa_3_s1));
endmodule
