// Logisim project somacompleta.circ as structural Verilog
module HA (
  input  a,
  input  b,
  output s0,
  output s1
);

  xor xor_1 (s0, a, b);
  and and_1 (s1, a, b);
endmodule

module HA_maior (
  input  in_1,
  input  in_2,
  output out_3,
  output out_4
);

  wire not_1_out, or_1_out;

  or or_1 (or_1_out, in_2, in_1);
  and and_1 (out_4, in_2, in_1);
  not not_1 (not_1_out, out_4);
  and and_2 (out_3, or_1_out, not_1_out);
endmodule

module FA_1bit (
  input  vai_um,
  input  a,
  input  b,
  output s0,
  output s1
);

  wire ha_1_s0, ha_1_s1, ha_2_s1;

  HA ha_1 (.a(a), .b(b), .s0(ha_1_s0), .s1(ha_1_s1));
  HA ha_2 (.a(vai_um), .b(ha_1_s0), .s0(s0), .s1(ha_2_s1));
  or or_1 (s1, ha_2_s1, ha_1_s1);

  // Notes on the sheet:
  //   2
  //   1
endmodule

module FA_4bits (
  input  [3:0] a,
  input  [3:0] b,
  output [4:0] s
);

  wire fa_1bit_1_s1, fa_1bit_2_s1, ha_1_s1;

  HA ha_1 (.a(a[0]), .b(b[0]), .s0(s[0]), .s1(ha_1_s1));
  FA_1bit fa_1bit_1 (.vai_um(ha_1_s1), .a(a[1]), .b(b[1]), .s0(s[1]), .s1(fa_1bit_1_s1));
  FA_1bit fa_1bit_2 (.vai_um(fa_1bit_1_s1), .a(a[2]), .b(b[2]), .s0(s[2]), .s1(fa_1bit_2_s1));
  FA_1bit fa_1bit_3 (.vai_um(fa_1bit_2_s1), .a(a[3]), .b(b[3]), .s0(s[3]), .s1(s[4]));
endmodule
