// Logisim project diferencacompleta3bits.circ as structural Verilog: 3 circuits, main circuit main
module main (
  input  a1,
  input  b1,
  input  a2,
  input  b2,
  input  a3,
  input  b3,
  output s1,
  output s2,
  output s3
);

  wire diferenca_completa_1_s1, meia_diferenca_1_s1;

  meia_diferenca meia_diferenca_1 (.x(a1), .y(b1), .s0(s1), .s1(meia_diferenca_1_s1));
  diferenca_completa diferenca_completa_1 (
    .e1(meia_diferenca_1_s1), .x(a2), .y(b2), .s0(s2), .s1(diferenca_completa_1_s1));
  diferenca_completa diferenca_completa_2 (.e1(diferenca_completa_1_s1), .x(a3), .y(b3), .s0(s3));  // open: s1

  // Notes on the sheet:
  //   Karen Alves - 407451
  //   Diferenca Comple com 3 bits
  //   C1
  //   C2
endmodule

module meia_diferenca (
  input  x,
  input  y,
  output s0,
  output s1
);

  wire not_1_out;

  not not_1 (not_1_out, x);
  xor s (s0, x, y);
  and a (s1, not_1_out, y);

  // Notes on the sheet:
  //   Meia diferenca
  //   Karen Alves - 407451
endmodule

module diferenca_completa (
  input  e1,
  input  x,
  input  y,
  output s0,
  output s1
);

  wire a_out, not_1_out, not_2_out, s_out, v2_out;

  xor s (s_out, x, y);
  not not_1 (not_1_out, x);
  and a (a_out, not_1_out, y);
  not not_2 (not_2_out, s_out);
  xor u_s0 (s0, e1, s_out);
  and v2 (v2_out, e1, not_2_out);
  or u_s1 (s1, v2_out, a_out);

  // Notes on the sheet:
  //   Karen Alves - 407451
  //   Diferenca completa
endmodule
