// Logisim project somacompleta4bits.circ as structural Verilog: 3 circuits, main circuit main
module main (
  input  a1,
  input  b1,
  input  a2,
  input  b2,
  input  a3,
  input  b3,
  input  a4,
  input  b4,
  output s1,
  output s2,
  output s3,
  output s4,
  output C4
);

  wire fulladder_1_carry, fulladder_2_carry, halfadder_1_v1;

  halfadder halfadder_1 (.a(a1), .b(b1), .soma(s1), .v1(halfadder_1_v1));
  fulladder fulladder_1 (.a(halfadder_1_v1), .b(a2), .c(b2), .carry(fulladder_1_carry), .soma(s2));
  fulladder fulladder_2 (.a(fulladder_1_carry), .b(a3), .c(b3), .carry(fulladder_2_carry), .soma(s3));
  fulladder fulladder_3 (.a(fulladder_2_carry), .b(a4), .c(b4), .carry(C4), .soma(s4));

  // Notes on the sheet:
  //   Soma Completa com 4 bits
  //   Karen Alves - 407451
  //   C1
  //   C2
  //   C3
endmodule

module halfadder (
  input  a,
  input  b,
  output soma,
  output v1
);

  xor xor_1 (soma, a, b);
  and and_1 (v1, a, b);

  // Notes on the sheet:
  //   Karen Alves - 407451
  //   Meia Soma
endmodule

module fulladder (
  input  a,
  input  b,
  input  c,
  output carry,
  output soma
);

  wire halfadder_1_soma, halfadder_1_v1, halfadder_2_v1;

  halfadder halfadder_1 (.a(a), .b(b), .soma(halfadder_1_soma), .v1(halfadder_1_v1));
  halfadder halfadder_2 (.a(c), .b(halfadder_1_soma), .soma(soma), .v1(halfadder_2_v1));
  or or_1 (carry, halfadder_1_v1, halfadder_2_v1);

  // Notes on the sheet:
  //   Karen Alves - 407451
  //   Soma Completa
endmodule
