// Logisim project guia05.circ as structural Verilog: 13 circuits, main circuit meiasoma
module meiasoma (
  input  a,
  input  b,
  output soma,
  output carry
);

  xor xor_1 (soma, b, a);
  and and_1 (carry, a, b);
endmodule

module somacompleta (
  input  a,
  input  b,
  input  c,
  output carryout,
  output soma
);

  wire meiasoma_1_carry, meiasoma_1_soma, meiasoma_2_carry;

  meiasoma meiasoma_1 (.a(b), .b(a), .soma(meiasoma_1_soma), .carry(meiasoma_1_carry));
  meiasoma meiasoma_2 (.a(c), .b(meiasoma_1_soma), .soma(soma), .carry(meiasoma_2_carry));
  or or_1 (carryout, meiasoma_1_carry, meiasoma_2_carry);
endmodule

module guia05exericicio01 (
  input  a3,
  input  a2,
  input  a1,
  input  a0,
  input  b3,
  input  b2,
  input  b1,
  input  b0,
  output s30,
  output s31,
  output s20,
  output s10,
  output s00
);

  wire meiasoma_1_carry, somacompleta_2_carryout, somacompleta_3_carryout;

  somacompleta somacompleta_1 (.a(somacompleta_2_carryout), .b(b3), .c(a3), .carryout(s31), .soma(s30));
  somacompleta somacompleta_2 (
    .a(somacompleta_3_carryout), .b(b2), .c(a2), .carryout(somacompleta_2_carryout), .soma(s20));
  somacompleta somacompleta_3 (.a(meiasoma_1_carry), .b(b1), .c(a1), .carryout(somacompleta_3_carryout), .soma(s10));
  meiasoma meiasoma_1 (.a(b0), .b(a0), .soma(s00), .carry(meiasoma_1_carry));
endmodule

module \meiadiferença  (
  input  a,
  input  b,
  output \diferença ,
  output sinal
);

  wire not_1_out;

  xor xor_1 (\diferença , a, b);
  not not_1 (not_1_out, a);
  and and_1 (sinal, b, not_1_out);
endmodule

module diferencacompleta (
  input  a,
  input  b,
  input  c,
  output sinal,
  output \diferença 
);

  wire \meiadiferença_1_diferença , \meiadiferença_1_sinal , \meiadiferença_2_sinal ;

  \meiadiferença  \meiadiferença_1  (
    .a(b), .b(a), .\diferença (\meiadiferença_1_diferença ), .sinal(\meiadiferença_1_sinal ));
  \meiadiferença  \meiadiferença_2  (
    .a(c), .b(\meiadiferença_1_diferença ), .\diferença (\diferença ), .sinal(\meiadiferença_2_sinal ));
  or or_1 (sinal, \meiadiferença_1_sinal , \meiadiferença_2_sinal );
endmodule

module guia05exercicio02 (
  input  [2:0] a0a1a2,
  input  [2:0] b0b1b2,
  output s21,
  output s0,
  output s10,
  output s20
);

  wire diferencacompleta_1_sinal, \meiadiferença_1_sinal ;

  \meiadiferença  \meiadiferença_1  (.a(b0b1b2[0]), .b(a0a1a2[0]), .\diferença (s20), .sinal(\meiadiferença_1_sinal ));
  diferencacompleta diferencacompleta_1 (
    .a(\meiadiferença_1_sinal ), .b(b0b1b2[1]), .c(a0a1a2[1]), .sinal(diferencacompleta_1_sinal),
    .\diferença (s10));
  diferencacompleta diferencacompleta_2 (
    .a(diferencacompleta_1_sinal), .b(b0b1b2[2]), .c(a0a1a2[2]), .sinal(s0), .\diferença (s21));
endmodule

module somacompletanands (
  input  a,
  input  b,
  input  c,
  output soma,
  output carryout
);

  wire meiasomanands_1_carry, meiasomanands_2_carry, meiasomanands_2_soma;

  meiasomanands meiasomanands_1 (.a(meiasomanands_2_soma), .b(c), .soma(soma), .carry(meiasomanands_1_carry));
  meiasomanands meiasomanands_2 (.a(a), .b(b), .soma(meiasomanands_2_soma), .carry(meiasomanands_2_carry));
  or or_1 (carryout, meiasomanands_1_carry, meiasomanands_2_carry);
endmodule

module meiasomanands (
  input  a,
  input  b,
  output soma,
  output carry
);

  wire nand_1_out, nand_2_out, nand_3_out, nand_4_out;

  nand nand_1 (nand_1_out, b, a);
  nand nand_2 (nand_2_out, a, nand_1_out);
  nand nand_3 (nand_3_out, nand_1_out, b);
  nand nand_4 (nand_4_out, a, b);
  nand nand_5 (soma, nand_2_out, nand_3_out);
  nand nand_6 (carry, nand_4_out, nand_4_out);
endmodule

module guia05exercicio04 (
  input  [2:0] a0a1a2,
  input  [2:0] b0b1b2,
  output s0,
  output s01,
  output s20,
  output s21
);

  wire meiasomanands_1_carry, somacompletanands_1_carryout;

  meiasomanands meiasomanands_1 (.a(a0a1a2[0]), .b(b0b1b2[0]), .soma(s20), .carry(meiasomanands_1_carry));
  somacompletanands somacompletanands_1 (
    .a(a0a1a2[1]), .b(b0b1b2[1]), .c(meiasomanands_1_carry), .soma(s01),
    .carryout(somacompletanands_1_carryout));
  somacompletanands somacompletanands_2 (
    .a(a0a1a2[2]), .b(b0b1b2[2]), .c(somacompletanands_1_carryout), .soma(s0), .carryout(s21));
endmodule

module guia05exercicio03 (
  input  a0,
  input  b0,
  input  a0_2,
  input  b1,
  input  a1,
  input  b1_2,
  input  a2,
  input  b1_3,
  input  a1_2,
  input  b0_2,
  input  a2_2,
  input  b1_4,
  input  a2_3,
  input  b2,
  input  a1_3,
  input  b2_2,
  input  a0_3,
  input  b2_3,
  output s0,
  output s1,
  output s2,
  output s3,
  output s4,
  output carry
);

  wire and_2_out, and_3_out, and_4_out, and_5_out, and_6_out, and_7_out, and_8_out, and_9_out,
       guia05exericicio01_1_s00, guia05exericicio01_1_s10, guia05exericicio01_1_s20, guia05exericicio01_1_s31;

  and and_1 (s0, a0, b0);
  and and_2 (and_2_out, a0_2, b1);
  and and_3 (and_3_out, a1, b1_2);
  and and_4 (and_4_out, a2, b1_3);
  and and_5 (and_5_out, a1_2, b0_2);
  and and_6 (and_6_out, a2_2, b1_4);
  and and_7 (and_7_out, a2_3, b2);
  and and_8 (and_8_out, a1_3, b2_2);
  and and_9 (and_9_out, a0_3, b2_3);
  guia05exericicio01 guia05exericicio01_1 (
    .a3(1'b0), .a2(1'b0), .a1(and_6_out), .a0(and_5_out), .b3(1'b0), .b2(and_4_out), .b1(and_3_out),
    .b0(and_2_out), .s31(guia05exericicio01_1_s31), .s20(guia05exericicio01_1_s20),
    .s10(guia05exericicio01_1_s10), .s00(guia05exericicio01_1_s00));  // open: s30
  guia05exericicio01 guia05exericicio01_2 (
    .a3(1'b0), .a2(and_9_out), .a1(and_8_out), .a0(and_7_out), .b3(guia05exericicio01_1_s31),
    .b2(guia05exericicio01_1_s20), .b1(guia05exericicio01_1_s10), .b0(guia05exericicio01_1_s00), .s30(carry),
    .s31(s4), .s20(s3), .s10(s2), .s00(s1));
endmodule

module \meiadiferençanor  (
  input  a,
  input  b,
  output diferenca,
  output sinal
);

  wire nor_1_out, nor_2_out, nor_3_out, nor_4_out, nor_5_out, nor_6_out, nor_7_out;

  nor nor_1 (nor_1_out, a, a);
  nor nor_2 (nor_2_out, b, b);
  nor nor_3 (nor_3_out, a, b);
  nor nor_4 (nor_4_out, a, a);
  nor nor_5 (nor_5_out, nor_1_out, nor_2_out);
  nor nor_6 (nor_6_out, b, b);
  nor nor_7 (nor_7_out, nor_4_out, nor_4_out);
  nor nor_8 (diferenca, nor_5_out, nor_3_out);
  nor nor_9 (sinal, nor_6_out, nor_7_out);
endmodule

module diferencanor (
  input  a,
  input  b,
  input  c,
  output diferenca,
  output sinal
);

  wire \meiadiferençanor_1_diferenca , \meiadiferençanor_1_sinal , \meiadiferençanor_2_sinal ;

  \meiadiferençanor  \meiadiferençanor_1  (
    .a(a), .b(b), .diferenca(\meiadiferençanor_1_diferenca ), .sinal(\meiadiferençanor_1_sinal ));
  \meiadiferençanor  \meiadiferençanor_2  (
    .a(c), .b(\meiadiferençanor_1_diferenca ), .diferenca(diferenca), .sinal(\meiadiferençanor_2_sinal ));
  or or_1 (sinal, \meiadiferençanor_1_sinal , \meiadiferençanor_2_sinal );
endmodule

module guia05exercicio05 (
  input  [2:0] a0a1a2,
  input  [2:0] b0b1b2,
  output s1,
  output s2,
  output s3,
  output sinal
);

  wire diferencanor_1_sinal, \meiadiferençanor_1_sinal ;

  \meiadiferençanor  \meiadiferençanor_1  (
    .a(a0a1a2[0]), .b(b0b1b2[0]), .diferenca(s1), .sinal(\meiadiferençanor_1_sinal ));
  diferencanor diferencanor_1 (
    .a(a0a1a2[1]), .b(b0b1b2[1]), .c(\meiadiferençanor_1_sinal ), .diferenca(s2), .sinal(diferencanor_1_sinal));
  diferencanor diferencanor_2 (.a(a0a1a2[2]), .b(b0b1b2[2]), .c(diferencanor_1_sinal), .diferenca(s3), .sinal(sinal));

  // Notes on the sheet:
  //   a
  //   b
endmodule
