// Logisim project circuitos_guia05.circ as structural Verilog: 12 circuits, main circuit fullAdder
module halfAdder (
  input  a,
  input  b,
  output s0,
  output s1
);

  xor xor_1 (s0, a, b);
  and and_1 (s1, a, b);

  // Notes on the sheet:
  //   Paulo Henrique de Almeida Amorim
  //   Meia soma
endmodule

module fullAdder (
  input  Cin,
  input  a,
  input  b,
  output Soma,
  output Cout
);

  wire halfadder_1_s0, halfadder_1_s1, halfadder_2_s1;

  halfAdder halfadder_1 (.a(a), .b(b), .s0(halfadder_1_s0), .s1(halfadder_1_s1));
  halfAdder halfadder_2 (.a(Cin), .b(halfadder_1_s0), .s0(Soma), .s1(halfadder_2_s1));
  or or_1 (Cout, halfadder_2_s1, halfadder_1_s1);

  // Notes on the sheet:
  //   Paulo Henrique de Almeida Amorim
  //   Soma completa
endmodule

module fullAdder4bits (
  input  a0,
  input  b0,
  input  a1,
  input  b1,
  input  a2,
  input  b2,
  input  a3,
  input  b3,
  output s0,
  output s1,
  output s2,
  output s3,
  output Cout
);

  wire fulladder_1_cout, fulladder_2_cout, halfadder_1_s1;

  halfAdder halfadder_1 (.a(a0), .b(b0), .s0(s0), .s1(halfadder_1_s1));
  fullAdder fulladder_1 (.Cin(halfadder_1_s1), .a(a1), .b(b1), .Soma(s1), .Cout(fulladder_1_cout));
  fullAdder fulladder_2 (.Cin(fulladder_1_cout), .a(a2), .b(b2), .Soma(s2), .Cout(fulladder_2_cout));
  fullAdder fulladder_3 (.Cin(fulladder_2_cout), .a(a3), .b(b3), .Soma(s3), .Cout(Cout));

  // Notes on the sheet:
  //   Paulo Henrique de Almeida Amorim
  //   Soma completa com 4 bits
endmodule

module halfDifference (
  input  a,
  input  b,
  output s0,
  output s1
);

  wire not_1_out;

  not not_1 (not_1_out, a);
  and and_1 (s0, not_1_out, b);
  xor xor_1 (s1, a, b);

  // Notes on the sheet:
  //   Paulo Henrique de Almeida Amorim
  //   Meia Diferença
endmodule

module fullDifference (
  input  Cin,
  input  a,
  input  b,
  output \Diferença ,
  output cout
);

  wire halfdifference_1_s0, halfdifference_1_s1, halfdifference_2_s0;

  halfDifference halfdifference_1 (.a(a), .b(b), .s0(halfdifference_1_s0), .s1(halfdifference_1_s1));
  halfDifference halfdifference_2 (.a(halfdifference_1_s1), .b(Cin), .s0(halfdifference_2_s0), .s1(\Diferença ));
  or or_1 (cout, halfdifference_1_s0, halfdifference_2_s0);

  // Notes on the sheet:
  //   Paulo Henrique de Almeida Amorim
  //   Diferença completa
endmodule

module fullDifference3bits (
  input  a0,
  input  b0,
  input  a1,
  input  b1,
  input  a2,
  input  b2,
  output s0,
  output s1,
  output s2,
  output Cout
);

  wire fulldifference_1_cout, halfdifference_1_s1;

  halfDifference halfdifference_1 (.a(a0), .b(b0), .s0(s0), .s1(halfdifference_1_s1));
  fullDifference fulldifference_1 (
    .Cin(halfdifference_1_s1), .a(a1), .b(b1), .\Diferença (s1), .cout(fulldifference_1_cout));
  fullDifference fulldifference_2 (.Cin(fulldifference_1_cout), .a(a2), .b(b2), .\Diferença (s2), .cout(Cout));

  // Notes on the sheet:
  //   Paulo Henrique de Almeida Amorim
  //   Diferença completa com 3 bits
endmodule

module halfAdderNAND (
  input  a,
  input  b,
  output s0,
  output s1
);

  wire temp1_out, temp2_out, temp3_out, temp5_out;

  nand temp1 (temp1_out, a, b);
  nand temp2 (temp2_out, a, temp1_out);
  nand temp3 (temp3_out, temp1_out, b);
  nand temp5 (temp5_out, b, a);
  nand temp4 (s0, temp2_out, temp3_out);
  nand temp6 (s1, temp5_out, temp5_out);

  // Notes on the sheet:
  //   Paulo Henrique de Almeida Amorim
  //   Meia soma
endmodule

module fullAdder2 (
  input  Cin,
  input  a,
  input  b,
  output Soma,
  output Cout
);

  wire halfaddernand_1_s0, halfaddernand_1_s1, halfaddernand_2_s1;

  halfAdderNAND halfaddernand_1 (.a(a), .b(b), .s0(halfaddernand_1_s0), .s1(halfaddernand_1_s1));
  halfAdderNAND halfaddernand_2 (.a(Cin), .b(halfaddernand_1_s0), .s0(Soma), .s1(halfaddernand_2_s1));
  or or_1 (Cout, halfaddernand_2_s1, halfaddernand_1_s1);

  // Notes on the sheet:
  //   Paulo Henrique de Almeida Amorim
  //   Soma completa
endmodule

module fullAdder3bits (
  input  a0,
  input  b0,
  input  a1,
  input  b1,
  input  a2,
  input  b2,
  output s0,
  output s1,
  output s2,
  output Cout
);

  wire fulladder2_1_cout, halfaddernand_1_s1;

  halfAdderNAND halfaddernand_1 (.a(a0), .b(b0), .s0(s0), .s1(halfaddernand_1_s1));
  fullAdder2 fulladder2_1 (.Cin(halfaddernand_1_s1), .a(a1), .b(b1), .Soma(s1), .Cout(fulladder2_1_cout));
  fullAdder2 fulladder2_2 (.Cin(fulladder2_1_cout), .a(a2), .b(b2), .Soma(s2), .Cout(Cout));

  // Notes on the sheet:
  //   Paulo Henrique de Almeida Amorim
  //   Soma completa com 3 bits
endmodule

module halfDifferenceNOR (
  input  a,
  input  b,
  output s0,
  output s1
);

  wire temp1_out, temp2_out, temp3_out, temp4_out, temp6_out, temp7_out, temp8_out;

  nor temp1 (temp1_out, a, b);
  nor temp7 (temp7_out, a, a);
  nor temp2 (temp2_out, a, temp1_out);
  nor temp3 (temp3_out, temp1_out, b);
  nor temp6 (temp6_out, b, b);
  nor temp8 (temp8_out, temp7_out, temp7_out);
  nor temp4 (temp4_out, temp2_out, temp3_out);
  nor temp5 (s0, temp4_out, temp4_out);
  nor temp9 (s1, temp6_out, temp8_out);

  // Notes on the sheet:
  //   Paulo Henrique de Almeida Amorim
  //   Diferença completa
endmodule

module fullDifference3bitsNOR (
  input  a0,
  input  b0,
  input  a1,
  input  b1,
  input  a2,
  input  b2,
  output s0,
  output s1,
  output s2,
  output Cout
);

  wire fulldifference2_1_cout, halfdifferencenor_1_s1;

  halfDifferenceNOR halfdifferencenor_1 (.a(a0), .b(b0), .s0(s0), .s1(halfdifferencenor_1_s1));
  fullDifference2 fulldifference2_1 (
    .Cin(halfdifferencenor_1_s1), .a(a1), .b(b1), .\Diferença (s1), .cout(fulldifference2_1_cout));
  fullDifference2 fulldifference2_2 (.Cin(fulldifference2_1_cout), .a(a2), .b(b2), .\Diferença (s2), .cout(Cout));

  // Notes on the sheet:
  //   Paulo Henrique de Almeida Amorim
  //   Diferença completa com 3 bits
endmodule

module fullDifference2 (
  input  Cin,
  input  a,
  input  b,
  output \Diferença ,
  output cout
);

  wire halfdifferencenor_1_s0, halfdifferencenor_1_s1, halfdifferencenor_2_s0;

  halfDifferenceNOR halfdifferencenor_1 (.a(a), .b(b), .s0(halfdifferencenor_1_s0), .s1(halfdifferencenor_1_s1));
  halfDifferenceNOR halfdifferencenor_2 (
    .a(halfdifferencenor_1_s1), .b(Cin), .s0(halfdifferencenor_2_s0), .s1(\Diferença ));
  or or_1 (cout, halfdifferencenor_1_s0, halfdifferencenor_2_s0);

  // Notes on the sheet:
  //   Paulo Henrique de Almeida Amorim
  //   Diferença completa
endmodule
