// Logisim project Simulaçoes Guia 05.circ as structural Verilog: 14 circuits, main circuit meia-soma
module meia_somaNAND (
  input  a,
  input  b,
  output s0,
  output s1
);

  wire temp1_out, temp2_out, temp3_out, temp4_out;

  nand temp1 (temp1_out, a, b);
  nand temp4 (temp4_out, b, a);
  nand temp2 (temp2_out, a, temp1_out);
  nand temp3 (temp3_out, temp1_out, b);
  nand temp5 (s0, temp4_out, temp4_out);
  nand temp4_2 (s1, temp2_out, temp3_out);

  // Notes on the sheet:
  //   Silvino Henrique Santos de Souza - 412773
  //   Circuito Meia - Soma usando Somente NANDs
  //   temp5 = s0
  //   temp 4 = s1
endmodule

module meia_soma (
  input  a,
  input  b,
  output s0,
  output s1
);

  and and_1 (s0, b, a);
  xor xor_1 (s1, a, b);

  // Notes on the sheet:
  //   Silvino Henrique Santos de Souza - 412773
  //   Meia -Soma Compacto
endmodule

module Somador_Completo (
  input  a,
  input  b,
  input  Cin,
  output Cout,
  output Soma
);

  wire meia_soma_1_s0, meia_soma_1_s1, meia_soma_2_s0;

  or or_1 (Cout, meia_soma_1_s0, meia_soma_2_s0);
  meia_soma meia_soma_1 (.a(a), .b(b), .s0(meia_soma_1_s0), .s1(meia_soma_1_s1));
  meia_soma meia_soma_2 (.a(meia_soma_1_s1), .b(Cin), .s0(meia_soma_2_s0), .s1(Soma));

  // Notes on the sheet:
  //   Silvino Henrique Santos de Souza - 412773
  //   Somador Completo 
endmodule

module Somador_Completo2 (
  input  a,
  input  b,
  input  Cin,
  output Cout,
  output Soma
);

  wire meia_somanand_1_s0, meia_somanand_1_s1, meia_somanand_2_s0;

  meia_somaNAND meia_somanand_1 (.a(a), .b(b), .s0(meia_somanand_1_s0), .s1(meia_somanand_1_s1));
  or or_1 (Cout, meia_somanand_1_s0, meia_somanand_2_s0);
  meia_somaNAND meia_somanand_2 (.a(meia_somanand_1_s1), .b(Cin), .s0(meia_somanand_2_s0), .s1(Soma));

  // Notes on the sheet:
  //   Silvino Henrique Santos de Souza - 412773
  //   Somador Completo (subcircuito com NANDs)
endmodule

module Somador_Completo3bits (
  input  b2,
  input  a2,
  input  b1,
  input  a1,
  input  b0,
  input  a0,
  output Cout,
  output s20,
  output s10,
  output s00
);

  wire meia_somanand_1_s0, somador_completo2_2_cout;

  Somador_Completo2 somador_completo2_1 (.a(a2), .b(b2), .Cin(somador_completo2_2_cout), .Cout(Cout), .Soma(s20));
  Somador_Completo2 somador_completo2_2 (
    .a(a1), .b(b1), .Cin(meia_somanand_1_s0), .Cout(somador_completo2_2_cout), .Soma(s10));
  meia_somaNAND meia_somanand_1 (.a(a0), .b(b0), .s0(meia_somanand_1_s0), .s1(s00));

  // Notes on the sheet:
  //   Silvino Henrique Santos de Souza - 412773
  //   Somador de 3Bits(com NAND's)
  //   Guia05 - 04
endmodule

module Somador_Completo4bits (
  input  b3,
  input  a3,
  input  b2,
  input  a2,
  input  b1,
  input  a1,
  input  b0,
  input  a0,
  output Cout,
  output s30,
  output s20,
  output s10,
  output s00
);

  wire meia_soma_1_s0, somador_completo_2_cout, somador_completo_3_cout;

  Somador_Completo somador_completo_1 (.a(a3), .b(b3), .Cin(somador_completo_2_cout), .Cout(Cout), .Soma(s30));
  Somador_Completo somador_completo_2 (
    .a(a2), .b(b2), .Cin(somador_completo_3_cout), .Cout(somador_completo_2_cout), .Soma(s20));
  Somador_Completo somador_completo_3 (
    .a(a1), .b(b1), .Cin(meia_soma_1_s0), .Cout(somador_completo_3_cout), .Soma(s10));
  meia_soma meia_soma_1 (.a(a0), .b(b0), .s0(meia_soma_1_s0), .s1(s00));

  // Notes on the sheet:
  //   Silvino Henrique Santos de Souza - 412773
  //   Somador de 4Bits
  //   Guia05 - 01
endmodule

module \meia_diferençaNOR  (
  input  a,
  input  b,
  output s0,
  output s1
);

  wire temp1_out, temp2_out, temp3_out, temp4_out, temp5_out, temp6_out, temp7_out;

  nor temp5 (temp5_out, a, a);
  nor temp1 (temp1_out, a, b);
  nor temp2 (temp2_out, a, temp1_out);
  nor temp3 (temp3_out, temp1_out, b);
  nor temp6 (temp6_out, temp5_out, temp5_out);
  nor temp7 (temp7_out, b, b);
  nor temp4 (temp4_out, temp2_out, temp3_out);
  nor nor_1 (s0, temp6_out, temp7_out);
  nor nor_2 (s1, temp4_out, temp4_out);

  // Notes on the sheet:
  //   Silvino Henrique Santos de Souza - 412773
  //   Meia-Diferença somente com NORs
endmodule

module \meia_diferença  (
  input  a,
  input  b,
  output s0,
  output s1
);

  wire not_1_out;

  and and_1 (s0, b, not_1_out);
  not not_1 (not_1_out, a);
  xor xor_1 (s1, a, b);

  // Notes on the sheet:
  //   Silvino Henrique Santos de Souza - 412773
  //   Meia - Diferença Compacto
endmodule

module \meia_diferençaNAND  (
  input  a,
  input  b,
  output s0,
  output s1
);

  wire temp1_out, temp2_out, temp3_out, temp4_out, temp5_out;

  nand temp4 (temp4_out, a, a);
  nand temp1 (temp1_out, a, b);
  nand temp5 (temp5_out, b, temp4_out);
  nand temp2 (temp2_out, a, temp1_out);
  nand temp3 (temp3_out, temp1_out, b);
  nand nand_1 (s0, temp5_out, temp5_out);
  nand nand_2 (s1, temp2_out, temp3_out);

  // Notes on the sheet:
  //   Silvino Henrique Santos de Souza - 412773
  //   Circuito Meia - Diferença usando Somente NANDs
endmodule

module Subtrator_Completo (
  input  a,
  input  b,
  input  Cin,
  output Cout,
  output \Diferença 
);

  wire \meia_diferença_1_s0 , \meia_diferença_1_s1 , \meia_diferença_2_s0 ;

  or or_1 (Cout, \meia_diferença_1_s0 , \meia_diferença_2_s0 );
  \meia_diferença  \meia_diferença_1  (.a(a), .b(b), .s0(\meia_diferença_1_s0 ), .s1(\meia_diferença_1_s1 ));
  \meia_diferença  \meia_diferença_2  (
    .a(\meia_diferença_1_s1 ), .b(Cin), .s0(\meia_diferença_2_s0 ), .s1(\Diferença ));

  // Notes on the sheet:
  //   Cin: pull=down
  //   Silvino Henrique Santos de Souza - 412773
  //   Subtrator Completo 
endmodule

module Subtrator_Completo2 (
  input  a,
  input  b,
  input  Cin,
  output Cout,
  output \Diferença 
);

  wire \meia_diferençanand_1_s0 , \meia_diferençanand_1_s1 , \meia_diferençanand_2_s0 ;

  \meia_diferençaNAND  \meia_diferençanand_1  (
    .a(a), .b(b), .s0(\meia_diferençanand_1_s0 ), .s1(\meia_diferençanand_1_s1 ));
  or or_1 (Cout, \meia_diferençanand_1_s0 , \meia_diferençanand_2_s0 );
  \meia_diferençaNAND  \meia_diferençanand_2  (
    .a(\meia_diferençanand_1_s1 ), .b(Cin), .s0(\meia_diferençanand_2_s0 ), .s1(\Diferença ));

  // Notes on the sheet:
  //   Cin: pull=down
  //   Silvino Henrique Santos de Souza - 412773
  //   Subtrator Completo (subcircuito com NANDs)
endmodule

module Subtrator_Completo3 (
  input  a,
  input  b,
  input  Cin,
  output Cout,
  output \Diferença 
);

  wire \meia_diferençanor_1_s0 , \meia_diferençanor_2_s0 , \meia_diferençanor_2_s1 ;

  or or_1 (Cout, \meia_diferençanor_2_s0 , \meia_diferençanor_1_s0 );
  \meia_diferençaNOR  \meia_diferençanor_1  (
    .a(\meia_diferençanor_2_s1 ), .b(Cin), .s0(\meia_diferençanor_1_s0 ), .s1(\Diferença ));
  \meia_diferençaNOR  \meia_diferençanor_2  (
    .a(a), .b(b), .s0(\meia_diferençanor_2_s0 ), .s1(\meia_diferençanor_2_s1 ));

  // Notes on the sheet:
  //   Cin: pull=down
  //   Silvino Henrique Santos de Souza - 412773
  //   Subtrator Completo (subcircuito com NORs)
endmodule

module Subtrator_Completo3bits (
  input  b2,
  input  a2,
  input  b1,
  input  a1,
  input  b0,
  input  a0,
  output Cout,
  output s20,
  output s10,
  output s00
);

  wire \meia_diferença_1_s0 , subtrator_completo_2_cout;

  Subtrator_Completo subtrator_completo_1 (
    .a(a2), .b(b2), .Cin(subtrator_completo_2_cout), .Cout(Cout), .\Diferença (s20));
  Subtrator_Completo subtrator_completo_2 (
    .a(a1), .b(b1), .Cin(\meia_diferença_1_s0 ), .Cout(subtrator_completo_2_cout), .\Diferença (s10));
  \meia_diferença  \meia_diferença_1  (.a(a0), .b(b0), .s0(\meia_diferença_1_s0 ), .s1(s00));

  // Notes on the sheet:
  //   Silvino Henrique Santos de Souza - 412773
  //   Subtrator de 3Bits
  //   Guia05 - 02
endmodule

module Subtrator_Completo3bitsNOR (
  input  b2,
  input  a2,
  input  b1,
  input  a1,
  input  b0,
  input  a0,
  output Cout,
  output s20,
  output s10,
  output s00
);

  wire \meia_diferençanor_1_s0 , subtrator_completo3_2_cout;

  Subtrator_Completo3 subtrator_completo3_1 (
    .a(a2), .b(b2), .Cin(subtrator_completo3_2_cout), .Cout(Cout), .\Diferença (s20));
  Subtrator_Completo3 subtrator_completo3_2 (
    .a(a1), .b(b1), .Cin(\meia_diferençanor_1_s0 ), .Cout(subtrator_completo3_2_cout), .\Diferença (s10));
  \meia_diferençaNOR  \meia_diferençanor_1  (.a(a0), .b(b0), .s0(\meia_diferençanor_1_s0 ), .s1(s00));

  // Notes on the sheet:
  //   Silvino Henrique Santos de Souza - 412773
  //   Subtrator de 3Bits
  //   Guia05 - 05
endmodule
