// Logisim project meiasoma.circ as structural Verilog: 1 circuit, main circuit main
module main (
  input  a,
  input  b,
  output s1,
  output s2
);

  and and_1 (s1, b, a);
  xor xor_1 (s2, a, b);
endmodule
