// Logisim project Guia_05.circ as structural Verilog: 7 circuits, main circuit Half Adder
module Half_Adder (
  input  A,
  input  B,
  output s1,
  output s0
);

  wire nor_1_out, nor_2_out, nor_3_out, nor_4_out, nor_5_out, nor_6_out, nor_8_out;

  nor nor_1 (nor_1_out, A, A);
  nor nor_2 (nor_2_out, B, B);
  nor nor_3 (nor_3_out, A, A);
  nor nor_4 (nor_4_out, B, B);
  nor nor_5 (nor_5_out, nor_3_out, B);
  nor nor_6 (nor_6_out, nor_4_out, A);
  nor nor_7 (s1, nor_1_out, nor_2_out);
  nor nor_8 (nor_8_out, nor_5_out, nor_6_out);
  nor nor_9 (s0, nor_8_out, nor_8_out);

  // Notes on the sheet:
  //   Aluno: Alyson Deives
  //   Matricula: 416589
  //   Guia 04_01 - Half Adder with NOR gates
endmodule

module Full_Adder (
  input  A,
  input  B,
  input  C,
  output s1,
  output s0
);

  wire half_adder_1_s0, half_adder_1_s1, half_adder_2_s1;

  Half_Adder half_adder_1 (.A(B), .B(A), .s1(half_adder_1_s1), .s0(half_adder_1_s0));
  Half_Adder half_adder_2 (.A(C), .B(half_adder_1_s0), .s1(half_adder_2_s1), .s0(s0));
  or or_1 (s1, half_adder_1_s1, half_adder_2_s1);

  // Notes on the sheet:
  //   Aluno: Alyson Deives
  //   Matricula: 416589
  //   Guia 04_02 - Full Adder with NOR gates
endmodule

module Half_Subtractor (
  input  A,
  input  B,
  output s1,
  output s0
);

  wire nor_1_out, nor_2_out, nor_3_out, nor_4_out, nor_5_out, nor_7_out;

  nor nor_1 (nor_1_out, B, B);
  nor nor_2 (nor_2_out, A, A);
  nor nor_3 (nor_3_out, B, B);
  nor nor_4 (nor_4_out, nor_2_out, B);
  nor nor_5 (nor_5_out, nor_3_out, A);
  nor nor_6 (s1, A, nor_1_out);
  nor nor_7 (nor_7_out, nor_4_out, nor_5_out);
  nor nor_8 (s0, nor_7_out, nor_7_out);

  // Notes on the sheet:
  //   Aluno: Alyson Deives
  //   Matricula: 416589
  //   Guia 03_05 - Half Differ with NOR gates
endmodule

module Full_Subtractor (
  input  A,
  input  B,
  input  C,
  output s1,
  output s0
);

  wire half_subtractor_1_s0, half_subtractor_1_s1, half_subtractor_2_s1;

  Half_Subtractor half_subtractor_1 (.A(A), .B(B), .s1(half_subtractor_1_s1), .s0(half_subtractor_1_s0));
  Half_Subtractor half_subtractor_2 (.A(half_subtractor_1_s0), .B(C), .s1(half_subtractor_2_s1), .s0(s0));
  or or_1 (s1, half_subtractor_1_s1, half_subtractor_2_s1);

  // Notes on the sheet:
  //   Aluno: Alyson Deives
  //   Matricula: 416589
  //   Guia 04_03 - Half Differ with NOR gates
endmodule

module Ex_01 (
  input  a3,
  input  a2,
  input  a1,
  input  a0,
  input  b3,
  input  b2,
  input  b1,
  input  b0,
  output s3,
  output s2,
  output s1,
  output s0,
  output s4
);

  wire full_adder_2_s1, full_adder_3_s1, half_adder_1_s1;

  Full_Adder full_adder_1 (.A(a3), .B(b3), .C(full_adder_2_s1), .s1(s4), .s0(s3));
  Full_Adder full_adder_2 (.A(a2), .B(b2), .C(full_adder_3_s1), .s1(full_adder_2_s1), .s0(s2));
  Full_Adder full_adder_3 (.A(a1), .B(b1), .C(half_adder_1_s1), .s1(full_adder_3_s1), .s0(s1));
  Half_Adder half_adder_1 (.A(a0), .B(b0), .s1(half_adder_1_s1), .s0(s0));

  // Notes on the sheet:
  //   Guia 05_01 - Full Adder 4 bits
  //   Aluno: Alyson Deives
  //   Matricula: 416589
endmodule

module Ex_02 (
  input  a2,
  input  a1,
  input  a0,
  input  b2,
  input  b1,
  input  b0,
  output s2,
  output s3,
  output s1,
  output s0
);

  wire full_subtractor_2_s1, half_subtractor_1_s1;

  Full_Subtractor full_subtractor_1 (.A(a2), .B(b2), .C(full_subtractor_2_s1), .s1(s2), .s0(s3));
  Full_Subtractor full_subtractor_2 (.A(a1), .B(b1), .C(half_subtractor_1_s1), .s1(full_subtractor_2_s1), .s0(s1));
  Half_Subtractor half_subtractor_1 (.A(a0), .B(b0), .s1(half_subtractor_1_s1), .s0(s0));

  // Notes on the sheet:
  //   Guia 05_02 - Full Subtractor 3 bits
  //   Aluno: Alyson Deives
  //   Matricula: 416589
endmodule

module Ex_03 (
  input  a2,
  input  a1,
  input  a0,
  input  b2,
  input  b1,
  input  b0,
  output s0,
  output s5,
  output s4,
  output s3,
  output s2,
  output s1
);

  wire and_2_out, and_3_out, and_4_out, and_5_out, and_6_out, and_7_out, and_8_out, and_9_out, ex_01_1_s0,
       ex_01_1_s1, ex_01_1_s2, ex_01_1_s3;

  and and_1 (s0, a0, b0);
  and and_2 (and_2_out, a1, b0);
  and and_3 (and_3_out, a2, b0);
  and and_4 (and_4_out, a0, b1);
  and and_5 (and_5_out, a1, b1);
  and and_6 (and_6_out, a2, b1);
  and and_7 (and_7_out, a0, b2);
  and and_8 (and_8_out, a1, b2);
  and and_9 (and_9_out, a2, b2);
  Ex_01 ex_01_1 (
    .a3(1'b0), .b3(1'b0), .a2(and_6_out), .b2(1'b0), .a1(and_5_out), .b1(and_3_out), .a0(and_4_out),
    .b0(and_2_out), .s3(ex_01_1_s3), .s2(ex_01_1_s2), .s1(ex_01_1_s1), .s0(ex_01_1_s0));  // open: s4
  Ex_01 ex_01_2 (
    .a3(and_9_out), .s4(s5), .b3(ex_01_1_s3), .a2(and_8_out), .b2(ex_01_1_s2), .a1(and_7_out),
    .b1(ex_01_1_s1), .a0(1'b0), .b0(ex_01_1_s0), .s3(s4), .s2(s3), .s1(s2), .s0(s1));

  // Notes on the sheet:
  //   Guia 05_03 - Multiplier 3 bits
  //   Aluno: Alyson Deives
  //   Matricula: 416589
endmodule
