// Logisim project Subtrator4b.circ as structural Verilog: 3 circuits, main circuit main
module main (
  input  a,
  input  b,
  output Vout,
  output d
);

  wire not_1_out;

  and and_1 (Vout, not_1_out, b);
  not not_1 (not_1_out, a);
  xor xor_1 (d, a, b);

  // Notes on the sheet:
  //   Meia diferença
endmodule

module HS (
  input  a,
  input  b,
  input  Vin,
  output Vout,
  output d
);

  wire main_1_d, main_1_vout, main_2_vout;

  or or_1 (Vout, main_1_vout, main_2_vout);
  main main_1 (.Vout(main_1_vout), .a(a), .b(b), .d(main_1_d));
  main main_2 (.Vout(main_2_vout), .a(main_1_d), .b(Vin), .d(d));

  // Notes on the sheet:
  //   Diferença completa
endmodule

module FS (
  input  a2,
  input  b2,
  input  a1,
  input  b1,
  input  a0,
  input  b0,
  output Vout,
  output d2,
  output d1,
  output d0
);

  wire hs_2_vout, main_1_vout;

  HS hs_1 (.Vout(Vout), .a(a2), .b(b2), .d(d2), .Vin(hs_2_vout));
  HS hs_2 (.Vout(hs_2_vout), .a(a1), .b(b1), .d(d1), .Vin(main_1_vout));
  main main_1 (.Vout(main_1_vout), .a(a0), .b(b0), .d(d0));

  // Notes on the sheet:
  //   subtrator de 4 bits
endmodule
