// Logisim project multiplicador3b.circ as structural Verilog: 3 circuits, main circuit main
module main (
  input  x,
  input  y,
  output Vout,
  output s
);

  and and_1 (Vout, y, x);
  xor xor_1 (s, x, y);
endmodule

module HA (
  input  x,
  input  y,
  input  Vin,
  output Vout,
  output s
);

  wire main_1_s, main_1_vout, main_2_vout;

  or or_1 (Vout, main_1_vout, main_2_vout);
  main main_1 (.Vout(main_1_vout), .x(x), .y(y), .s(main_1_s));
  main main_2 (.Vout(main_2_vout), .x(main_1_s), .y(Vin), .s(s));
endmodule

module FA (
  input  a0,
  input  b0,
  input  a1,
  input  b1,
  input  a2,
  input  b2,
  output Vout,
  output p4,
  output p3,
  output p2,
  output p1,
  output p0
);

  wire and_1_out, and_2_out, and_3_out, and_4_out, and_5_out, and_6_out, and_7_out, and_8_out, ha_2_s,
       ha_2_vout, ha_3_s, ha_3_vout, main_1_vout, main_2_vout, main_3_vout;

  and and_1 (and_1_out, a2, b2);
  and and_2 (and_2_out, a1, b2);
  HA ha_1 (.Vout(Vout), .x(ha_2_vout), .y(main_1_vout), .s(p4), .Vin(and_1_out));
  main main_1 (.Vout(main_1_vout), .x(ha_2_s), .y(and_2_out), .s(p3));
  and and_3 (and_3_out, a2, b1);
  HA ha_2 (.Vout(ha_2_vout), .x(main_2_vout), .y(ha_3_vout), .s(ha_2_s), .Vin(and_3_out));
  and and_4 (and_4_out, b2, a0);
  and and_5 (and_5_out, b1, a1);
  main main_2 (.Vout(main_2_vout), .x(ha_3_s), .y(and_4_out), .s(p2));
  and and_6 (and_6_out, b0, a2);
  HA ha_3 (.Vout(ha_3_vout), .x(main_3_vout), .y(and_6_out), .s(ha_3_s), .Vin(and_5_out));
  and and_7 (and_7_out, b1, a0);
  main main_3 (.Vout(main_3_vout), .x(and_8_out), .y(and_7_out), .s(p1));
  and and_8 (and_8_out, a1, b0);
  and and_9 (p0, b0, a0);

  // Notes on the sheet:
  //   t9
  //   v4
  //   t7
  //   v3
  //   t8
  //   t6
  //   t4
  //   v1
  //   v1
  //   v2
  //   t3
  //   t2
  //   t5
  //   v0
  //   t1
  //   t0
endmodule
