// Logisim project somador3bNand.circ as structural Verilog: 3 circuits, main circuit main
module main (
  input  x,
  input  y,
  output Vout,
  output s
);

  wire nand_1_out, nand_2_out, nand_3_out, nand_4_out, nand_5_out, nand_7_out, nand_8_out, nand_9_out,
       nand_10_out;

  nand nand_1 (nand_1_out, x, x);
  nand nand_2 (nand_2_out, nand_1_out, y);
  nand nand_3 (nand_3_out, nand_2_out, nand_2_out);
  nand nand_4 (nand_4_out, nand_3_out, nand_3_out);
  nand nand_5 (nand_5_out, nand_8_out, nand_8_out);
  nand nand_6 (s, nand_4_out, nand_5_out);
  nand nand_7 (nand_7_out, x, nand_9_out);
  nand nand_8 (nand_8_out, nand_7_out, nand_7_out);
  nand nand_9 (nand_9_out, y, y);
  nand nand_10 (nand_10_out, x, y);
  nand nand_11 (Vout, nand_10_out, nand_10_out);

  // Notes on the sheet:
  //   Meio somador de nand
endmodule

module HA (
  input  x,
  input  y,
  input  Vin,
  output Vout,
  output s
);

  wire main_1_s, main_1_vout, main_2_vout;

  main main_1 (.x(x), .y(y), .s(main_1_s), .Vout(main_1_vout));
  main main_2 (.x(Vin), .y(main_1_s), .s(s), .Vout(main_2_vout));
  or or_1 (Vout, main_1_vout, main_2_vout);

  // Notes on the sheet:
  //   Somador completo
endmodule

module FA (
  input  a2,
  input  b2,
  input  a1,
  input  b1,
  input  a0,
  input  b0,
  output Vout,
  output s2,
  output s1,
  output s0
);

  wire ha_1_vout, main_1_vout;

  main main_1 (.x(a2), .y(b2), .s(s2), .Vout(main_1_vout));
  HA ha_1 (.Vin(main_1_vout), .x(a1), .y(b1), .s(s1), .Vout(ha_1_vout));
  HA ha_2 (.Vin(ha_1_vout), .x(a0), .y(b0), .s(s0), .Vout(Vout));

  // Notes on the sheet:
  //   Somador completo 3 bits
endmodule
