// Logisim project somador4b.circ as structural Verilog: 3 circuits, main circuit main
module main (
  input  x,
  input  y,
  output Vout,
  output s
);

  xor xor_1 (s, x, y);
  and and_1 (Vout, y, x);
endmodule

module HA (
  input  x,
  input  y,
  input  Vin,
  output Vout,
  output s
);

  wire main_1_s, main_1_vout, main_2_vout;

  main main_1 (.x(x), .y(y), .s(main_1_s), .Vout(main_1_vout));
  main main_2 (.x(Vin), .y(main_1_s), .s(s), .Vout(main_2_vout));
  or or_1 (Vout, main_1_vout, main_2_vout);
endmodule

module FA (
  input  a3,
  input  b3,
  input  a2,
  input  b2,
  input  a1,
  input  b1,
  input  a0,
  input  b0,
  output Vout,
  output s3,
  output s2,
  output s1,
  output s0
);

  wire ha_1_vout, ha_2_vout, main_1_vout;

  main main_1 (.x(a3), .y(b3), .s(s3), .Vout(main_1_vout));
  HA ha_1 (.Vin(main_1_vout), .x(a2), .y(b2), .s(s2), .Vout(ha_1_vout));
  HA ha_2 (.Vin(ha_1_vout), .x(a1), .y(b1), .s(s1), .Vout(ha_2_vout));
  HA ha_3 (.Vin(ha_2_vout), .x(a0), .y(b0), .s(s0), .Vout(Vout));

  // Notes on the sheet:
  //   Somador completo de 4 bits
endmodule
