// Logisim project subtator3bNor.circ as structural Verilog: 3 circuits, main circuit main
module main (
  input  a,
  input  b,
  output Vout,
  output d
);

  wire nor_2_out, nor_3_out, nor_4_out, nor_5_out, nor_6_out, nor_7_out, nor_9_out;

  nor nor_1 (Vout, nor_2_out, nor_3_out);
  nor nor_2 (nor_2_out, b, b);
  nor nor_3 (nor_3_out, nor_4_out, nor_4_out);
  nor nor_4 (nor_4_out, a, a);
  nor nor_5 (nor_5_out, a, a);
  nor nor_6 (nor_6_out, nor_5_out, nor_7_out);
  nor nor_7 (nor_7_out, b, b);
  nor nor_8 (d, nor_6_out, nor_9_out);
  nor nor_9 (nor_9_out, b, a);

  // Notes on the sheet:
  //   Meia diferença de nor
endmodule

module HS (
  input  a,
  input  b,
  input  Vin,
  output Vout,
  output d
);

  wire main_1_d, main_1_vout, main_2_vout;

  or or_1 (Vout, main_1_vout, main_2_vout);
  main main_1 (.Vout(main_1_vout), .a(a), .b(b), .d(main_1_d));
  main main_2 (.Vout(main_2_vout), .a(main_1_d), .b(Vin), .d(d));
endmodule

module FS (
  input  a2,
  input  b2,
  input  a1,
  input  b1,
  input  a0,
  input  b0,
  output Vout,
  output d2,
  output d1,
  output d0
);

  wire hs_2_vout, main_1_vout;

  HS hs_1 (.Vout(Vout), .a(a2), .b(b2), .d(d2), .Vin(hs_2_vout));
  HS hs_2 (.Vout(hs_2_vout), .a(a1), .b(b1), .d(d1), .Vin(main_1_vout));
  main main_1 (.Vout(main_1_vout), .a(a0), .b(b0), .d(d0));

  // Notes on the sheet:
  //   Subtrator de 3 bits nor
endmodule
