// Logisim project Guia05.circ as structural Verilog: 13 circuits, main circuit Half Adder
module Half_Adder (
  input  a,
  input  b,
  output Soma,
  output Cout
);

  xor xor_1 (Soma, a, b);
  and and_1 (Cout, a, b);

  // Notes on the sheet:
  //   Douglas de Loredo Borges - 417889
endmodule

module Full_Adder (
  input  a,
  input  b,
  input  Cin,
  output Soma,
  output Cout
);

  wire half_adder_1_cout, half_adder_1_soma, half_adder_2_cout;

  Half_Adder half_adder_1 (.Soma(half_adder_1_soma), .Cout(half_adder_1_cout), .a(a), .b(b));
  Half_Adder half_adder_2 (.Soma(Soma), .Cout(half_adder_2_cout), .a(half_adder_1_soma), .b(Cin));
  or or_1 (Cout, half_adder_2_cout, half_adder_1_cout);

  // Notes on the sheet:
  //   Douglas de Loredo Borges - 417889
endmodule

module Ex01___Full_Adder_4_Bits (
  input  [3:0] a,
  input  [3:0] b,
  output [4:0] Soma
);

  wire full_adder_1_cout, full_adder_2_cout, half_adder_1_cout;

  Half_Adder half_adder_1 (.Soma(Soma[0]), .Cout(half_adder_1_cout), .a(a[0]), .b(b[0]));
  Full_Adder full_adder_1 (.Soma(Soma[1]), .Cout(full_adder_1_cout), .a(a[1]), .b(b[1]), .Cin(half_adder_1_cout));
  Full_Adder full_adder_2 (.Soma(Soma[2]), .Cout(full_adder_2_cout), .a(a[2]), .b(b[2]), .Cin(full_adder_1_cout));
  Full_Adder full_adder_3 (.Soma(Soma[3]), .Cout(Soma[4]), .a(a[3]), .b(b[3]), .Cin(full_adder_2_cout));

  // Notes on the sheet:
  //   Douglas de Loredo Borges - 417889
endmodule

module Half_Subtractor (
  input  a,
  input  b,
  output \Diferença ,
  output Vout
);

  wire not_1_out;

  xor xor_1 (\Diferença , a, b);
  not not_1 (not_1_out, a);
  and and_1 (Vout, not_1_out, b);

  // Notes on the sheet:
  //   Douglas de Loredo Borges - 417889
endmodule

module Full_Subtractor (
  input  a,
  input  b,
  input  Vin,
  output \Diferença ,
  output Vout
);

  wire \half_subtractor_1_diferença , half_subtractor_1_vout, half_subtractor_2_vout;

  Half_Subtractor half_subtractor_1 (
    .\Diferença (\half_subtractor_1_diferença ), .Vout(half_subtractor_1_vout), .a(a), .b(b));
  Half_Subtractor half_subtractor_2 (
    .\Diferença (\Diferença ), .Vout(half_subtractor_2_vout), .a(\half_subtractor_1_diferença ), .b(Vin));
  or or_1 (Vout, half_subtractor_2_vout, half_subtractor_1_vout);

  // Notes on the sheet:
  //   Douglas de Loredo Borges - 417889
endmodule

module Ex02___Full_Subtractor_3_Bits (
  input  [2:0] a,
  input  [2:0] b,
  output [3:0] \Subtração_com_Sinal 
);

  wire full_subtractor_1_vout, half_subtractor_1_vout;

  Half_Subtractor half_subtractor_1 (
    .\Diferença (\Subtração_com_Sinal [0]), .Vout(half_subtractor_1_vout), .a(a[0]), .b(b[0]));
  Full_Subtractor full_subtractor_1 (
    .\Diferença (\Subtração_com_Sinal [1]), .Vout(full_subtractor_1_vout), .a(a[1]), .b(b[1]),
    .Vin(half_subtractor_1_vout));
  Full_Subtractor full_subtractor_2 (
    .\Diferença (\Subtração_com_Sinal [2]), .Vout(\Subtração_com_Sinal [3]), .a(a[2]), .b(b[2]),
    .Vin(full_subtractor_1_vout));

  // Notes on the sheet:
  //   Douglas de Loredo Borges - 417889
endmodule

module Ex03___Multiplier_3_Bits (
  input  [2:0] a,
  input  [2:0] b,
  output [5:0] Produto
);

  wire [1:0] and_1_out;
  wire [2:0] and_3_out;
  wire [3:1] and_6_out;
  wire [4:0] ex01_full_adder_4_bits_1_soma;

  and and_1 (and_1_out[0], b[0], a[1]);
  and and_2 (and_1_out[1], b[0], a[2]);
  and and_3 (and_3_out[0], b[1], a[0]);
  and and_4 (and_3_out[1], b[1], a[1]);
  and and_5 (and_3_out[2], b[1], a[2]);
  Ex01___Full_Adder_4_Bits ex01_full_adder_4_bits_1 (
    .Soma(ex01_full_adder_4_bits_1_soma), .a({2'b00, and_1_out}), .b({1'b0, and_3_out}));
  and and_6 (and_6_out[1], b[2], a[0]);
  and and_7 (and_6_out[2], b[2], a[1]);
  and and_8 (and_6_out[3], b[2], a[2]);
  and and_9 (Produto[0], b[0], a[0]);
  Ex01___Full_Adder_4_Bits ex01_full_adder_4_bits_2 (
    .Soma(Produto[5:1]), .a(ex01_full_adder_4_bits_1_soma[3:0]), .b({and_6_out, 1'b0}));

  // Notes on the sheet:
  //   Douglas de Loredo Borges - 417889
endmodule

module Half_Adder_Nand (
  input  a,
  input  b,
  output Soma,
  output Cout
);

  wire nand_1_out, nand_2_out, nand_3_out, nand_4_out, nand_5_out;

  nand nand_1 (nand_1_out, a, a);
  nand nand_2 (nand_2_out, b, b);
  nand nand_3 (nand_3_out, b, a);
  nand nand_4 (nand_4_out, nand_1_out, nand_2_out);
  nand nand_5 (nand_5_out, nand_4_out, nand_3_out);
  nand nand_6 (Cout, nand_3_out, nand_3_out);
  nand nand_7 (Soma, nand_5_out, nand_5_out);

  // Notes on the sheet:
  //   Douglas de Loredo Borges - 417889
endmodule

module Full_Adder_Nand (
  input  a,
  input  b,
  input  Cin,
  output Soma,
  output Cout
);

  wire half_adder_nand_1_cout, half_adder_nand_1_soma, half_adder_nand_2_cout, nand_1_out, nand_2_out;

  Half_Adder_Nand half_adder_nand_1 (.Soma(half_adder_nand_1_soma), .Cout(half_adder_nand_1_cout), .a(a), .b(b));
  Half_Adder_Nand half_adder_nand_2 (.Soma(Soma), .Cout(half_adder_nand_2_cout), .a(half_adder_nand_1_soma), .b(Cin));
  nand nand_1 (nand_1_out, half_adder_nand_2_cout, half_adder_nand_2_cout);
  nand nand_2 (nand_2_out, half_adder_nand_1_cout, half_adder_nand_1_cout);
  nand nand_3 (Cout, nand_1_out, nand_2_out);

  // Notes on the sheet:
  //   Douglas de Loredo Borges - 417889
endmodule

module Ex04___Full_Adder_3_Bits_Nand (
  input  [2:0] a,
  input  [2:0] b,
  output [3:0] Soma
);

  wire full_adder_nand_1_cout, half_adder_nand_1_cout;

  Half_Adder_Nand half_adder_nand_1 (.Soma(Soma[0]), .Cout(half_adder_nand_1_cout), .a(a[0]), .b(b[0]));
  Full_Adder_Nand full_adder_nand_1 (
    .Soma(Soma[1]), .Cout(full_adder_nand_1_cout), .a(a[1]), .b(b[1]), .Cin(half_adder_nand_1_cout));
  Full_Adder_Nand full_adder_nand_2 (.Soma(Soma[2]), .Cout(Soma[3]), .a(a[2]), .b(b[2]), .Cin(full_adder_nand_1_cout));

  // Notes on the sheet:
  //   Douglas de Loredo Borges - 417889
endmodule

module Half_Subtractor_Nor (
  input  a,
  input  b,
  output \Diferença ,
  output Vout
);

  wire nor_1_out, nor_2_out, nor_3_out, nor_4_out, nor_5_out;

  nor nor_1 (nor_1_out, a, a);
  nor nor_2 (nor_2_out, nor_1_out, nor_3_out);
  nor nor_3 (nor_3_out, b, b);
  nor nor_4 (nor_4_out, a, b);
  nor nor_5 (nor_5_out, b, b);
  nor nor_6 (Vout, nor_5_out, a);
  nor nor_7 (\Diferença , nor_2_out, nor_4_out);

  // Notes on the sheet:
  //   Douglas de Loredo Borges - 417889
endmodule

module Full_Subtractor_Nor (
  input  a,
  input  b,
  input  Vin,
  output \Diferença ,
  output Vout
);

  wire \half_subtractor_nor_1_diferença , half_subtractor_nor_1_vout, half_subtractor_nor_2_vout, nor_1_out;

  Half_Subtractor_Nor half_subtractor_nor_1 (
    .\Diferença (\half_subtractor_nor_1_diferença ), .Vout(half_subtractor_nor_1_vout), .a(a), .b(b));
  Half_Subtractor_Nor half_subtractor_nor_2 (
    .\Diferença (\Diferença ), .Vout(half_subtractor_nor_2_vout), .a(\half_subtractor_nor_1_diferença ),
    .b(Vin));
  nor nor_1 (nor_1_out, half_subtractor_nor_2_vout, half_subtractor_nor_1_vout);
  nor nor_2 (Vout, nor_1_out, nor_1_out);

  // Notes on the sheet:
  //   Douglas de Loredo Borges - 417889
endmodule

module Ex05___Full_Subtractor_3_Bits_Nor (
  input  [2:0] a,
  input  [2:0] b,
  output [3:0] \Subtração_com_Sinal 
);

  wire full_subtractor_nor_1_vout, half_subtractor_nor_1_vout;

  Half_Subtractor_Nor half_subtractor_nor_1 (
    .\Diferença (\Subtração_com_Sinal [0]), .Vout(half_subtractor_nor_1_vout), .a(a[0]), .b(b[0]));
  Full_Subtractor_Nor full_subtractor_nor_1 (
    .\Diferença (\Subtração_com_Sinal [1]), .Vout(full_subtractor_nor_1_vout), .a(a[1]), .b(b[1]),
    .Vin(half_subtractor_nor_1_vout));
  Full_Subtractor_Nor full_subtractor_nor_2 (
    .\Diferença (\Subtração_com_Sinal [2]), .Vout(\Subtração_com_Sinal [3]), .a(a[2]), .b(b[2]),
    .Vin(full_subtractor_nor_1_vout));

  // Notes on the sheet:
  //   Douglas de Loredo Borges - 417889
endmodule
