// Logisim project Guia05.circ as structural Verilog: 6 circuits, main circuit Meia-Diferença
module \Meia_Diferença  (
  input  a,
  input  b,
  output s0,
  output s1
);

  wire not_1_out;

  xor xor_1 (s0, a, b);
  not not_1 (not_1_out, a);
  and and_1 (s1, b, not_1_out);

  // Notes on the sheet:
  //   Operador Meia-Diferança
endmodule

module \Diferença_completa  (
  input  a,
  input  b,
  input  Vin,
  output s1,
  output s0
);

  wire \meia_diferença_1_s0 , \meia_diferença_1_s1 , \meia_diferença_2_s1 ;

  \Meia_Diferença  \meia_diferença_1  (.a(a), .b(b), .s0(\meia_diferença_1_s0 ), .s1(\meia_diferença_1_s1 ));
  \Meia_Diferença  \meia_diferença_2  (.a(Vin), .b(\meia_diferença_1_s0 ), .s0(s0), .s1(\meia_diferença_2_s1 ));
  or or_1 (s1, \meia_diferença_1_s1 , \meia_diferença_2_s1 );

  // Notes on the sheet:
  //   Operador Diferença-Completa
endmodule

module Exercicio02 (
  input  [2:0] in_1,
  input  [2:0] in_2,
  output out_3,
  output out_4,
  output out_5,
  output out_6
);

  wire \diferença_completa_2_s0 , \meia_diferença_1_s1 ;

  \Diferença_completa  \diferença_completa_1  (
    .a(in_1[2]), .b(in_2[2]), .Vin(\diferença_completa_2_s0 ), .s1(out_5), .s0(out_4));
  \Diferença_completa  \diferença_completa_2  (
    .a(in_1[1]), .b(in_2[1]), .Vin(\meia_diferença_1_s1 ), .s1(out_6), .s0(\diferença_completa_2_s0 ));
  \Meia_Diferença  \meia_diferença_1  (.a(in_1[0]), .b(in_2[0]), .s0(out_3), .s1(\meia_diferença_1_s1 ));
endmodule

module Meia_Soma (
  input  a,
  input  b,
  output s0,
  output s1
);

  xor xor_1 (s0, a, b);
  and and_1 (s1, a, b);

  // Notes on the sheet:
  //   Operador Meia-Soma
endmodule

module Soma_Completa (
  input  a,
  input  b,
  input  c,
  output s0,
  output s1
);

  wire meia_soma_1_s0, meia_soma_1_s1, meia_soma_2_s1;

  Meia_Soma meia_soma_1 (.a(a), .b(b), .s0(meia_soma_1_s0), .s1(meia_soma_1_s1));
  Meia_Soma meia_soma_2 (.a(meia_soma_1_s0), .b(c), .s0(s0), .s1(meia_soma_2_s1));
  or or_1 (s1, meia_soma_2_s1, meia_soma_1_s1);

  // Notes on the sheet:
  //   Operador Soma-Completa
endmodule

module Exercicio01 (
  input  [3:0] a,
  input  [3:0] b,
  output out_3,
  output [3:0] out_4
);

  wire meia_soma_1_s1, soma_completa_2_s1, soma_completa_3_s1;

  Soma_Completa soma_completa_1 (.a(a[3]), .b(b[3]), .c(soma_completa_2_s1), .s0(out_4[3]), .s1(out_3));
  Soma_Completa soma_completa_2 (.a(a[2]), .b(b[2]), .c(soma_completa_3_s1), .s0(out_4[2]), .s1(soma_completa_2_s1));
  Soma_Completa soma_completa_3 (.a(a[1]), .b(b[1]), .c(meia_soma_1_s1), .s0(out_4[1]), .s1(soma_completa_3_s1));
  Meia_Soma meia_soma_1 (.a(a[0]), .b(b[0]), .s0(out_4[0]), .s1(meia_soma_1_s1));

  // Notes on the sheet:
  //   Operador Soma-Completa 4 Bits
endmodule
