// Logisim project Guia05_Circ.circ as structural Verilog: 12 circuits, main circuit halfAdder
module halfAdder (
  input  a,
  input  b,
  output s0,
  output s1
);

  xor xor_1 (s0, a, b);
  and and_1 (s1, a, b);

  // Notes on the sheet:
  //   Alvaro Henrique de Araujo Rungue - 395487
endmodule

module fullAdder (
  input  Cin,
  input  a,
  input  b,
  output Soma,
  output Cout
);

  wire halfadder_1_s0, halfadder_1_s1, halfadder_2_s1;

  halfAdder halfadder_1 (.a(a), .b(b), .s0(halfadder_1_s0), .s1(halfadder_1_s1));
  halfAdder halfadder_2 (.a(Cin), .b(halfadder_1_s0), .s0(Soma), .s1(halfadder_2_s1));
  or or_1 (Cout, halfadder_2_s1, halfadder_1_s1);

  // Notes on the sheet:
  //   Alvaro Henrique de Araujo Rungue - 395487
endmodule

module fullAdder4bits (
  input  a0,
  input  b0,
  input  a1,
  input  b1,
  input  a2,
  input  b2,
  input  a3,
  input  b3,
  output s0,
  output s1,
  output s2,
  output s3,
  output Cout
);

  wire fulladder_1_p5, fulladder_2_p6, halfadder_1_s1;

  halfAdder halfadder_1 (.a(a0), .b(b0), .s0(s0), .s1(halfadder_1_s1));
  // fullAdder fulladder_1: pin names not known; wires that end beside it: halfadder_1_s1, a1, b1, s1, fulladder_1_p5
  // fullAdder fulladder_2: pin names not known; wires that end beside it: fulladder_1_p5, a2, b2, fulladder_1_p5, s2, fulladder_2_p6
  // fullAdder fulladder_3: pin names not known; wires that end beside it: a3, b3, fulladder_2_p6, s3, Cout

  // Notes on the sheet:
  //   Alvaro Henrique de Araujo Rungue - 395487
endmodule

module halfsubtractor (
  input  a,
  input  b,
  output s0,
  output s1
);

  wire not_1_out;

  not not_1 (not_1_out, a);
  and and_1 (s0, not_1_out, b);
  xor xor_1 (s1, a, b);

  // Notes on the sheet:
  //   Alvaro Henrique de Araujo Rungue - 395487
endmodule

module fullSubtractor (
  input  Cin,
  input  a,
  input  b,
  output Diferenca,
  output cout
);

  wire halfsubtractor_1_s0, halfsubtractor_1_s1, halfsubtractor_2_s1;

  halfsubtractor halfsubtractor_1 (.a(a), .b(b), .s0(halfsubtractor_1_s0), .s1(halfsubtractor_1_s1));
  halfsubtractor halfsubtractor_2 (.a(Cin), .b(halfsubtractor_1_s1), .s0(Diferenca), .s1(halfsubtractor_2_s1));
  or or_1 (cout, halfsubtractor_1_s0, halfsubtractor_2_s1);

  // Notes on the sheet:
  //   Alvaro Henrique de Araujo Rungue - 395487
endmodule

module fullSubtractor3bits (
  input  a0,
  input  b0,
  input  a1,
  input  b1,
  input  a2,
  input  b2,
  output s0,
  output s1,
  output s2,
  output Cout
);

  wire fullsubtractor_1_cout, halfsubtractor_1_s1;

  halfsubtractor halfsubtractor_1 (.a(a0), .b(b0), .s0(s0), .s1(halfsubtractor_1_s1));
  fullSubtractor fullsubtractor_1 (
    .Cin(halfsubtractor_1_s1), .a(a1), .b(b1), .Diferenca(s1), .cout(fullsubtractor_1_cout));
  fullSubtractor fullsubtractor_2 (.Cin(fullsubtractor_1_cout), .a(a2), .b(b2), .Diferenca(s2), .cout(Cout));

  // Notes on the sheet:
  //   Alvaro Henrique de Araujo Rungue - 395487
endmodule

module halfAdderNAND (
  input  a,
  input  b,
  output s0,
  output s1
);

  wire nand_1_out, nand_2_out, nand_3_out, nand_4_out;

  nand nand_1 (nand_1_out, a, b);
  nand nand_2 (nand_2_out, a, nand_1_out);
  nand nand_3 (nand_3_out, nand_1_out, b);
  nand nand_4 (nand_4_out, b, a);
  nand nand_5 (s0, nand_2_out, nand_3_out);
  nand nand_6 (s1, nand_4_out, nand_4_out);

  // Notes on the sheet:
  //   Alvaro Henrique de Araujo Rungue - 395487
endmodule

module fullAdder2 (
  input  Cin,
  input  a,
  input  b,
  output Soma,
  output Cout
);

  wire halfaddernand_1_s0, halfaddernand_1_s1, halfaddernand_2_s1;

  halfAdderNAND halfaddernand_1 (.a(a), .b(b), .s0(halfaddernand_1_s0), .s1(halfaddernand_1_s1));
  halfAdderNAND halfaddernand_2 (.a(Cin), .b(halfaddernand_1_s0), .s0(Soma), .s1(halfaddernand_2_s1));
  or or_1 (Cout, halfaddernand_2_s1, halfaddernand_1_s1);

  // Notes on the sheet:
  //   Alvaro Henrique de Araujo Rungue - 395487
endmodule

module fullAdder3bits (
  input  a0,
  input  b0,
  input  a1,
  input  b1,
  input  a2,
  input  b2,
  output s0,
  output s1,
  output s2,
  output Cout
);

  wire fulladder2_1_cout, halfaddernand_1_s1;

  halfAdderNAND halfaddernand_1 (.a(a0), .b(b0), .s0(s0), .s1(halfaddernand_1_s1));
  fullAdder2 fulladder2_1 (.Cin(halfaddernand_1_s1), .a(a1), .b(b1), .Soma(s1), .Cout(fulladder2_1_cout));
  fullAdder2 fulladder2_2 (.Cin(fulladder2_1_cout), .a(a2), .b(b2), .Soma(s2), .Cout(Cout));

  // Notes on the sheet:
  //   Alvaro Henrique de Araujo Rungue - 395487
endmodule

module halfSubtractorNOR (
  input  a,
  input  b,
  output s0,
  output s1
);

  wire nor_1_out, nor_2_out, nor_3_out, nor_4_out, nor_5_out, nor_6_out, nor_7_out;

  nor nor_1 (nor_1_out, a, b);
  nor nor_2 (nor_2_out, a, a);
  nor nor_3 (nor_3_out, a, nor_1_out);
  nor nor_4 (nor_4_out, nor_1_out, b);
  nor nor_5 (nor_5_out, b, b);
  nor nor_6 (nor_6_out, nor_2_out, nor_2_out);
  nor nor_7 (nor_7_out, nor_3_out, nor_4_out);
  nor nor_8 (s0, nor_7_out, nor_7_out);
  nor nor_9 (s1, nor_5_out, nor_6_out);

  // Notes on the sheet:
  //   Alvaro Henrique de Araujo Rungue - 395487
endmodule

module fullSubtractor3bitsNOR (
  input  a0,
  input  b0,
  input  a1,
  input  b1,
  input  a2,
  input  b2,
  output s0,
  output s1,
  output s2,
  output Cout
);

  wire fullsubtractor2_1_cout, halfsubtractornor_1_s1;

  halfSubtractorNOR halfsubtractornor_1 (.a(a0), .b(b0), .s0(s0), .s1(halfsubtractornor_1_s1));
  fullSubtractor2 fullsubtractor2_1 (
    .Cin(halfsubtractornor_1_s1), .a(a1), .b(b1), .Diferenca(s1), .cout(fullsubtractor2_1_cout));
  fullSubtractor2 fullsubtractor2_2 (.Cin(fullsubtractor2_1_cout), .a(a2), .b(b2), .Diferenca(s2), .cout(Cout));

  // Notes on the sheet:
  //   Alvaro Henrique de Araujo Rungue - 395487
endmodule

module fullSubtractor2 (
  input  Cin,
  input  a,
  input  b,
  output Diferenca,
  output cout
);

  wire halfsubtractornor_1_s0, halfsubtractornor_1_s1, halfsubtractornor_2_s0;

  halfSubtractorNOR halfsubtractornor_1 (.a(a), .b(b), .s0(halfsubtractornor_1_s0), .s1(halfsubtractornor_1_s1));
  halfSubtractorNOR halfsubtractornor_2 (
    .a(halfsubtractornor_1_s1), .b(Cin), .s0(halfsubtractornor_2_s0), .s1(Diferenca));
  or or_1 (cout, halfsubtractornor_1_s0, halfsubtractornor_2_s0);

  // Notes on the sheet:
  //   Alvaro Henrique de Araujo Rungue - 395487
endmodule
