// Logisim project guia05.circ as structural Verilog: 13 circuits, main circuit meia soma
module meia_soma (
  input  e1,
  input  e2,
  output soma,
  output carry
);

  xor xor_1 (soma, e2, e1);
  and and_1 (carry, e1, e2);

  // Notes on the sheet:
  //   Anderson Belchior de Carvalho - 396673
endmodule

module soma_completa (
  input  e1,
  input  e2,
  input  e3,
  output carry_out,
  output soma
);

  wire meia_soma_1_carry, meia_soma_1_soma, meia_soma_2_carry;

  meia_soma meia_soma_1 (.e1(e1), .e2(e2), .soma(meia_soma_1_soma), .carry(meia_soma_1_carry));
  meia_soma meia_soma_2 (.e1(meia_soma_1_soma), .e2(e3), .soma(soma), .carry(meia_soma_2_carry));
  or or_1 (carry_out, meia_soma_1_carry, meia_soma_2_carry);

  // Notes on the sheet:
  //   Anderson Belchior de Carvalho - 396673
endmodule

module Exercicio01 (
  input  a3,
  input  a2,
  input  a1,
  input  a0,
  input  b3,
  input  b2,
  input  b1,
  input  b0,
  output s30,
  output s31,
  output s20,
  output s10,
  output s00
);

  wire meia_soma_1_carry, soma_completa_2_carry_out, soma_completa_3_carry_out;

  soma_completa soma_completa_1 (.e1(a3), .e2(b3), .e3(soma_completa_2_carry_out), .carry_out(s30), .soma(s31));
  soma_completa soma_completa_2 (
    .e1(a2), .e2(b2), .e3(soma_completa_3_carry_out), .carry_out(soma_completa_2_carry_out), .soma(s20));
  soma_completa soma_completa_3 (
    .e1(a1), .e2(b1), .e3(meia_soma_1_carry), .carry_out(soma_completa_3_carry_out), .soma(s10));
  meia_soma meia_soma_1 (.e1(a0), .e2(b0), .soma(s00), .carry(meia_soma_1_carry));

  // Notes on the sheet:
  //   Anderson Belchior de Carvalho - 396673
endmodule

module \meia_diferença  (
  input  e1,
  input  e2,
  output \diferença ,
  output sinal
);

  wire not_1_out;

  xor xor_1 (\diferença , e1, e2);
  not not_1 (not_1_out, e1);
  and and_1 (sinal, e2, not_1_out);

  // Notes on the sheet:
  //   Anderson Belchior de Carvalho - 396673
endmodule

module \diferença_completa  (
  input  e1,
  input  e2,
  input  e3,
  output sinal,
  output \diferença 
);

  wire \meia_diferença_1_diferença , \meia_diferença_1_sinal , \meia_diferença_2_sinal ;

  \meia_diferença  \meia_diferença_1  (
    .e1(e1), .e2(e2), .\diferença (\meia_diferença_1_diferença ), .sinal(\meia_diferença_1_sinal ));
  \meia_diferença  \meia_diferença_2  (
    .e1(\meia_diferença_1_diferença ), .e2(e3), .\diferença (\diferença ), .sinal(\meia_diferença_2_sinal ));
  or or_1 (sinal, \meia_diferença_1_sinal , \meia_diferença_2_sinal );

  // Notes on the sheet:
  //   temp1
  //   temp2
  //   Anderson Belchior de Carvalho - 396673
  //   temp3
endmodule

module Exercicio02 (
  input  [2:0] a0a1a2,
  input  [2:0] b0b1b2,
  output s21,
  output s0,
  output s10,
  output s20
);

  wire \diferença_completa_1_sinal , \meia_diferença_1_sinal ;

  \meia_diferença  \meia_diferença_1  (
    .e1(a0a1a2[0]), .e2(b0b1b2[0]), .\diferença (s20), .sinal(\meia_diferença_1_sinal ));
  \diferença_completa  \diferença_completa_1  (
    .e1(a0a1a2[1]), .e2(b0b1b2[1]), .e3(\meia_diferença_1_sinal ), .sinal(\diferença_completa_1_sinal ),
    .\diferença (s10));
  \diferença_completa  \diferença_completa_2  (
    .e1(a0a1a2[2]), .e2(b0b1b2[2]), .e3(\diferença_completa_1_sinal ), .sinal(s21), .\diferença (s0));

  // Notes on the sheet:
  //   Anderson Belchior de Carvalho - 396673
endmodule

module soma_completa_com_nand_s (
  input  e1,
  input  e2,
  input  e3,
  output soma,
  output carryout
);

  wire meia_soma_com_nan_s_1_carry, meia_soma_com_nan_s_2_carry, meia_soma_com_nan_s_2_soma;

  meia_soma_com_nan_s meia_soma_com_nan_s_1 (
    .e1(meia_soma_com_nan_s_2_soma), .e2(e3), .soma(soma), .carry(meia_soma_com_nan_s_1_carry));
  meia_soma_com_nan_s meia_soma_com_nan_s_2 (
    .e1(e1), .e2(e2), .soma(meia_soma_com_nan_s_2_soma), .carry(meia_soma_com_nan_s_2_carry));
  or or_1 (carryout, meia_soma_com_nan_s_1_carry, meia_soma_com_nan_s_2_carry);

  // Notes on the sheet:
  //   Anderson Belchior de Carvalho - 396673
  //   temp2
  //   temp1
  //   tem3
endmodule

module meia_soma_com_nan_s (
  input  e1,
  input  e2,
  output soma,
  output carry
);

  wire nand_1_out, nand_2_out, nand_3_out, nand_4_out;

  nand nand_1 (nand_1_out, e2, e1);
  nand nand_2 (nand_2_out, e1, nand_1_out);
  nand nand_3 (nand_3_out, nand_1_out, e2);
  nand nand_4 (nand_4_out, e1, e2);
  nand nand_5 (soma, nand_2_out, nand_3_out);
  nand nand_6 (carry, nand_4_out, nand_4_out);

  // Notes on the sheet:
  //   temp1
  //   temp1
  //   Anderson Belchior de Carvalho - 396673
  //   temp2
  //   temp3
  //   temp4
endmodule

module Extra04 (
  input  [2:0] a0a1a2,
  input  [2:0] b0b1b2,
  output s21,
  output s0,
  output s01,
  output s20
);

  wire meia_soma_com_nan_s_1_carry, soma_completa_com_nand_s_1_carryout;

  meia_soma_com_nan_s meia_soma_com_nan_s_1 (
    .e1(a0a1a2[0]), .e2(b0b1b2[0]), .soma(s20), .carry(meia_soma_com_nan_s_1_carry));
  soma_completa_com_nand_s soma_completa_com_nand_s_1 (
    .e1(a0a1a2[1]), .e2(b0b1b2[1]), .e3(meia_soma_com_nan_s_1_carry), .soma(s01),
    .carryout(soma_completa_com_nand_s_1_carryout));
  soma_completa_com_nand_s soma_completa_com_nand_s_2 (
    .e1(a0a1a2[2]), .e2(b0b1b2[2]), .e3(soma_completa_com_nand_s_1_carryout), .soma(s0), .carryout(s21));

  // Notes on the sheet:
  //   Anderson Belchior de Carvalho - 396673
endmodule

module Exercicio03 (
  input  a0,
  input  a0_2,
  input  b0,
  input  b1,
  input  a1,
  input  b1_2,
  input  a2,
  input  b1_3,
  input  a1_2,
  input  b0_2,
  input  a2_2,
  input  b1_4,
  input  a2_3,
  input  b2,
  input  a1_3,
  input  b2_2,
  input  a0_3,
  input  b2_3,
  output s0,
  output s4,
  output s1,
  output s2,
  output s3,
  output carry
);

  wire and_1_out, and_2_out, and_3_out, and_4_out, and_5_out, and_6_out, and_7_out, and_8_out,
       exercicio01_1_s00, exercicio01_1_s10, exercicio01_1_s20, exercicio01_1_s31;

  and and_1 (and_1_out, a0, b1);
  and and_2 (and_2_out, a1, b1_2);
  and and_3 (and_3_out, a2, b1_3);
  and and_4 (and_4_out, a1_2, b0_2);
  and and_5 (and_5_out, a2_2, b1_4);
  Exercicio01 exercicio01_1 (
    .a3(1'b0), .a2(1'b0), .a1(and_5_out), .a0(and_4_out), .b3(1'b0), .b2(and_3_out), .b1(and_2_out),
    .b0(and_1_out), .s31(exercicio01_1_s31), .s20(exercicio01_1_s20), .s10(exercicio01_1_s10),
    .s00(exercicio01_1_s00));  // open: s30
  and and_6 (and_6_out, a2_3, b2);
  and and_7 (and_7_out, a1_3, b2_2);
  and and_8 (and_8_out, a0_3, b2_3);
  and and_9 (s0, a0_2, b0);
  Exercicio01 exercicio01_2 (
    .a3(1'b0), .a2(and_8_out), .a1(and_7_out), .a0(and_6_out), .b3(exercicio01_1_s31),
    .b2(exercicio01_1_s20), .b1(exercicio01_1_s10), .b0(exercicio01_1_s00), .s30(carry), .s31(s3), .s20(s2),
    .s10(s1), .s00(s4));

  // Notes on the sheet:
  //   Anderson Belchior de Carvalho - 396673
endmodule

module \meia_diferença_com_nor  (
  input  e1,
  input  e2,
  output diferenca,
  output sinal
);

  wire nor_1_out, nor_2_out, nor_3_out, nor_4_out, nor_5_out, nor_6_out, nor_7_out;

  nor nor_1 (nor_1_out, e1, e1);
  nor nor_2 (nor_2_out, e2, e2);
  nor nor_3 (nor_3_out, e1, e2);
  nor nor_4 (nor_4_out, e1, e1);
  nor nor_5 (nor_5_out, nor_1_out, nor_2_out);
  nor nor_6 (nor_6_out, e2, e2);
  nor nor_7 (nor_7_out, nor_4_out, nor_4_out);
  nor nor_8 (diferenca, nor_5_out, nor_3_out);
  nor nor_9 (sinal, nor_6_out, nor_7_out);

  // Notes on the sheet:
  //   temp1
  //   temp2
  //   temp4
  //   temp6
  //   Anderson Belchior de Carvalho - 396673
  //   temp3
  //   temp5
  //   temp7
endmodule

module \diferença_completa_com_nor  (
  input  e1,
  input  e2,
  input  e3,
  output diferenca,
  output sinal
);

  wire \meia_diferença_com_nor_1_diferenca , \meia_diferença_com_nor_1_sinal ,
       \meia_diferença_com_nor_2_sinal ;

  \meia_diferença_com_nor  \meia_diferença_com_nor_1  (
    .e1(e1), .e2(e2), .diferenca(\meia_diferença_com_nor_1_diferenca ),
    .sinal(\meia_diferença_com_nor_1_sinal ));
  \meia_diferença_com_nor  \meia_diferença_com_nor_2  (
    .e1(\meia_diferença_com_nor_1_diferenca ), .e2(e3), .diferenca(diferenca),
    .sinal(\meia_diferença_com_nor_2_sinal ));
  or or_1 (sinal, \meia_diferença_com_nor_2_sinal , \meia_diferença_com_nor_1_sinal );

  // Notes on the sheet:
  //   temp1
  //   Anderson Belchior de Carvalho - 396673
  //   temp2
  //   temp3
endmodule

module Extra05 (
  input  [2:0] a0a1a2,
  input  [2:0] b0b1b2,
  output s21,
  output s0,
  output s10,
  output s20
);

  wire \diferença_completa_com_nor_1_sinal , \meia_diferença_com_nor_1_sinal ;

  \meia_diferença_com_nor  \meia_diferença_com_nor_1  (
    .e1(a0a1a2[0]), .e2(b0b1b2[0]), .diferenca(s20), .sinal(\meia_diferença_com_nor_1_sinal ));
  \diferença_completa_com_nor  \diferença_completa_com_nor_1  (
    .e1(a0a1a2[1]), .e2(b0b1b2[1]), .e3(\meia_diferença_com_nor_1_sinal ), .diferenca(s10),
    .sinal(\diferença_completa_com_nor_1_sinal ));
  \diferença_completa_com_nor  \diferença_completa_com_nor_2  (
    .e1(a0a1a2[2]), .e2(b0b1b2[2]), .e3(\diferença_completa_com_nor_1_sinal ), .diferenca(s0), .sinal(s21));

  // Notes on the sheet:
  //   e1
  //   e2
  //   Anderson Belchior de Carvalho - 396673
endmodule
