// Logisim project guia06.circ as structural Verilog: 8 circuits, main circuit MeioSomador
module ALU5_bits (
  input  [4:0] A,
  input  [4:0] B,
  input  [1:0] chave,
  output [5:0] Saida
);

  wire [5:0] comparador_1_comparador, somador5_bits_1_soma, subtrator5_bits_1_diferenca;

  Somador5_Bits somador5_bits_1 (.a(A), .b(B), .Soma(somador5_bits_1_soma));
  Comparador comparador_1 (.a(A), .b(B), .Comparador(comparador_1_comparador[0]));
  Subtrator5_Bits subtrator5_bits_1 (.a(A), .b(A), .Diferenca(subtrator5_bits_1_diferenca));
  Multiplexer #(.select(2), .width(6)) multiplexer_1 (
    .in0(somador5_bits_1_soma), .in1(comparador_1_comparador), .in2(subtrator5_bits_1_diferenca),
    .out(Saida), .sel(chave));  // open: in3

  // Notes on the sheet:
  //   Não sei fazer o resto dos exercicios !
  //   Larissa Fernandes Leijoto- 410476
endmodule

module MeioSomador (
  input  a,
  input  b,
  output Soma,
  output Carry
);

  and and_1 (Carry, b, a);
  xor xor_1 (Soma, a, b);
endmodule

module SomadorCompleto (
  input  a,
  input  b,
  input  c,
  output Soma,
  output CarryOut
);

  wire meiosomador_1_carry, meiosomador_1_soma, meiosomador_2_carry;

  MeioSomador meiosomador_1 (.a(a), .b(b), .Soma(meiosomador_1_soma), .Carry(meiosomador_1_carry));
  MeioSomador meiosomador_2 (.a(meiosomador_1_soma), .b(c), .Soma(Soma), .Carry(meiosomador_2_carry));
  or or_1 (CarryOut, meiosomador_2_carry, meiosomador_1_carry);
endmodule

module Somador5_Bits (
  input  [4:0] a,
  input  [4:0] b,
  output [5:0] Soma
);

  wire meiosomador_1_carry, somadorcompleto_2_carryout, somadorcompleto_3_carryout,
       somadorcompleto_4_carryout;

  SomadorCompleto somadorcompleto_1 (
    .a(a[4]), .b(b[4]), .c(somadorcompleto_3_carryout), .Soma(Soma[4]), .CarryOut(Soma[5]));
  SomadorCompleto somadorcompleto_2 (
    .a(a[2]), .b(b[2]), .c(somadorcompleto_4_carryout), .Soma(Soma[2]), .CarryOut(somadorcompleto_2_carryout));
  SomadorCompleto somadorcompleto_3 (
    .a(a[3]), .b(b[3]), .c(somadorcompleto_2_carryout), .Soma(Soma[3]), .CarryOut(somadorcompleto_3_carryout));
  SomadorCompleto somadorcompleto_4 (
    .a(a[1]), .b(b[1]), .c(meiosomador_1_carry), .Soma(Soma[1]), .CarryOut(somadorcompleto_4_carryout));
  MeioSomador meiosomador_1 (.a(a[0]), .b(b[0]), .Soma(Soma[0]), .Carry(meiosomador_1_carry));
endmodule

module MeioSubtrator (
  input  a,
  input  b,
  output diferenca,
  output Sinal
);

  wire not_1_out;

  not not_1 (not_1_out, a);
  xor xor_1 (diferenca, a, b);
  and and_1 (Sinal, not_1_out, b);
endmodule

module SubtratorCompleto (
  input  a,
  input  b,
  input  c,
  output diferenca,
  output Sinal
);

  wire meiosubtrator_1_diferenca, meiosubtrator_1_sinal, meiosubtrator_2_sinal;

  MeioSubtrator meiosubtrator_1 (.a(a), .b(b), .diferenca(meiosubtrator_1_diferenca), .Sinal(meiosubtrator_1_sinal));
  MeioSubtrator meiosubtrator_2 (
    .a(meiosubtrator_1_diferenca), .b(c), .diferenca(diferenca), .Sinal(meiosubtrator_2_sinal));
  or or_1 (Sinal, meiosubtrator_2_sinal, meiosubtrator_1_sinal);
endmodule

module Subtrator5_Bits (
  input  [4:0] a,
  input  [4:0] b,
  output [5:0] Diferenca
);

  wire meiosubtrator_1_sinal, subtratorcompleto_2_sinal, subtratorcompleto_3_sinal, subtratorcompleto_4_sinal;

  SubtratorCompleto subtratorcompleto_1 (
    .a(a[4]), .b(b[4]), .c(subtratorcompleto_2_sinal), .diferenca(Diferenca[4]), .Sinal(Diferenca[5]));
  SubtratorCompleto subtratorcompleto_2 (
    .a(a[3]), .b(b[3]), .c(subtratorcompleto_3_sinal), .diferenca(Diferenca[3]),
    .Sinal(subtratorcompleto_2_sinal));
  SubtratorCompleto subtratorcompleto_3 (
    .a(a[2]), .b(b[2]), .c(subtratorcompleto_4_sinal), .diferenca(Diferenca[2]),
    .Sinal(subtratorcompleto_3_sinal));
  SubtratorCompleto subtratorcompleto_4 (
    .a(a[1]), .b(b[1]), .c(meiosubtrator_1_sinal), .diferenca(Diferenca[1]), .Sinal(subtratorcompleto_4_sinal));
  MeioSubtrator meiosubtrator_1 (.a(a[0]), .b(b[0]), .diferenca(Diferenca[0]), .Sinal(meiosubtrator_1_sinal));
endmodule

module Comparador (
  input  [4:0] a,
  input  [4:0] b,
  output Comparador
);

  ExactlyOne xor_1 (
    .out(Comparador), .in0(b[4]), .in1(b[3]), .in2(b[2]), .in3(b[1]), .in4(b[0]), .in5(a[4]), .in6(a[3]),
    .in7(a[2]), .in8(a[1]), .in9(a[0]));
endmodule
