// Logisim project Guia06.circ as structural Verilog: 14 circuits, main circuit Half Adder
module Half_Adder (
  input  a,
  input  b,
  output Soma,
  output Cout
);

  xor xor_1 (Soma, a, b);
  and and_1 (Cout, a, b);

  // Notes on the sheet:
  //   Douglas de Loredo Borges - 417889
endmodule

module Full_Adder (
  input  a,
  input  b,
  input  Cin,
  output Soma,
  output Cout
);

  wire half_adder_1_cout, half_adder_1_soma, half_adder_2_cout;

  Half_Adder half_adder_1 (.Soma(half_adder_1_soma), .Cout(half_adder_1_cout), .a(a), .b(b));
  Half_Adder half_adder_2 (.Soma(Soma), .Cout(half_adder_2_cout), .a(half_adder_1_soma), .b(Cin));
  or or_1 (Cout, half_adder_2_cout, half_adder_1_cout);

  // Notes on the sheet:
  //   Douglas de Loredo Borges - 417889
endmodule

module Full_Adder_5_Bits (
  input  [4:0] a,
  input  [4:0] b,
  output [5:0] Soma
);

  wire full_adder_1_cout, full_adder_2_cout, full_adder_3_cout, half_adder_1_cout;

  Half_Adder half_adder_1 (.Soma(Soma[0]), .Cout(half_adder_1_cout), .a(a[0]), .b(b[0]));
  Full_Adder full_adder_1 (.Soma(Soma[1]), .Cout(full_adder_1_cout), .a(a[1]), .b(b[1]), .Cin(half_adder_1_cout));
  Full_Adder full_adder_2 (.Soma(Soma[2]), .Cout(full_adder_2_cout), .a(a[2]), .b(b[2]), .Cin(full_adder_1_cout));
  Full_Adder full_adder_3 (.Soma(Soma[3]), .Cout(full_adder_3_cout), .a(a[3]), .b(b[3]), .Cin(full_adder_2_cout));
  Full_Adder full_adder_4 (.Soma(Soma[4]), .Cout(Soma[5]), .a(a[4]), .b(b[4]), .Cin(full_adder_3_cout));

  // Notes on the sheet:
  //   Douglas de Loredo Borges - 417889
endmodule

module Half_Subtractor (
  input  a,
  input  b,
  output \Diferença ,
  output Vout
);

  wire not_1_out;

  xor xor_1 (\Diferença , a, b);
  not not_1 (not_1_out, a);
  and and_1 (Vout, not_1_out, b);

  // Notes on the sheet:
  //   Douglas de Loredo Borges - 417889
endmodule

module Full_Subtractor (
  input  a,
  input  b,
  input  Vin,
  output \Diferença ,
  output Vout
);

  wire \half_subtractor_1_diferença , half_subtractor_1_vout, half_subtractor_2_vout;

  Half_Subtractor half_subtractor_1 (
    .\Diferença (\half_subtractor_1_diferença ), .Vout(half_subtractor_1_vout), .a(a), .b(b));
  Half_Subtractor half_subtractor_2 (
    .\Diferença (\Diferença ), .Vout(half_subtractor_2_vout), .a(\half_subtractor_1_diferença ), .b(Vin));
  or or_1 (Vout, half_subtractor_2_vout, half_subtractor_1_vout);

  // Notes on the sheet:
  //   Douglas de Loredo Borges - 417889
endmodule

module Full_Subtractor_5_Bits (
  input  [4:0] a,
  input  [4:0] b,
  output [5:0] \Diferença 
);

  wire full_subtractor_1_vout, full_subtractor_2_vout, full_subtractor_3_vout, half_subtractor_1_vout;

  Half_Subtractor half_subtractor_1 (.\Diferença (\Diferença [0]), .Vout(half_subtractor_1_vout), .a(a[0]), .b(b[0]));
  Full_Subtractor full_subtractor_1 (
    .\Diferença (\Diferença [1]), .Vout(full_subtractor_1_vout), .a(a[1]), .b(b[1]),
    .Vin(half_subtractor_1_vout));
  Full_Subtractor full_subtractor_2 (
    .\Diferença (\Diferença [2]), .Vout(full_subtractor_2_vout), .a(a[2]), .b(b[2]),
    .Vin(full_subtractor_1_vout));
  Full_Subtractor full_subtractor_3 (
    .\Diferença (\Diferença [3]), .Vout(full_subtractor_3_vout), .a(a[3]), .b(b[3]),
    .Vin(full_subtractor_2_vout));
  Full_Subtractor full_subtractor_4 (
    .\Diferença (\Diferença [4]), .Vout(\Diferença [5]), .a(a[4]), .b(b[4]), .Vin(full_subtractor_3_vout));

  // Notes on the sheet:
  //   Douglas de Loredo Borges - 417889
endmodule

module Logic_Comparator_5_Bits (
  input  [4:0] a,
  input  [4:0] b,
  output a___b
);

  wire xnor_1_out, xnor_2_out, xnor_3_out, xnor_4_out, xnor_5_out;

  xnor xnor_1 (xnor_1_out, b[0], a[0]);
  xnor xnor_2 (xnor_2_out, a[1], b[1]);
  xnor xnor_3 (xnor_3_out, a[2], b[2]);
  xnor xnor_4 (xnor_4_out, a[3], b[3]);
  xnor xnor_5 (xnor_5_out, a[4], b[4]);
  and and_1 (a___b, xnor_1_out, xnor_2_out, xnor_3_out, xnor_4_out, xnor_5_out);

  // Notes on the sheet:
  //   Douglas de Loredo Borges - 417889
endmodule

module Signal_Flag (
  input  a4,
  input  b4,
  input  Op,
  input  s4,
  output Sinal
);

  wire and_1_out, and_2_out, and_3_out, and_4_out, and_5_out, not_1_out, not_2_out, not_3_out, not_4_out;

  and and_1 (and_1_out, a4, s4);
  and and_2 (and_2_out, a4, b4, not_1_out);
  not not_1 (not_1_out, Op);
  not not_2 (not_2_out, Op);
  and and_3 (and_3_out, b4, not_2_out, s4);
  not not_3 (not_3_out, b4);
  and and_4 (and_4_out, not_3_out, Op, s4);
  not not_4 (not_4_out, b4);
  and and_5 (and_5_out, a4, not_4_out, Op);
  or or_1 (Sinal, and_1_out, and_2_out, and_3_out, and_4_out, and_5_out);
endmodule

module Overflow_Flag (
  input  a4,
  input  b4,
  input  Op,
  input  s4,
  output Overflow
);

  wire and_1_out, and_2_out, and_3_out, and_4_out, not_1_out, not_2_out, not_3_out, not_4_out, not_5_out,
       not_6_out, not_7_out, not_8_out;

  and and_1 (and_1_out, a4, b4, not_1_out, not_2_out);
  not not_1 (not_1_out, Op);
  not not_2 (not_2_out, s4);
  not not_3 (not_3_out, a4);
  not not_4 (not_4_out, b4);
  and and_2 (and_2_out, not_3_out, not_4_out, not_5_out, s4);
  not not_5 (not_5_out, Op);
  not not_6 (not_6_out, a4);
  and and_3 (and_3_out, not_6_out, b4, Op, s4);
  not not_7 (not_7_out, b4);
  and and_4 (and_4_out, a4, not_7_out, Op, not_8_out);
  not not_8 (not_8_out, s4);
  or or_1 (Overflow, and_1_out, and_2_out, and_3_out, and_4_out);
endmodule

module Aritmetic_Comparator_B (
  input  a4,
  input  b4,
  input  s4,
  output b___a
);

  wire and_1_out, and_2_out, and_3_out, not_1_out, not_2_out;

  and and_1 (and_1_out, a4, not_1_out);
  not not_1 (not_1_out, b4);
  and and_2 (and_2_out, a4, s4);
  not not_2 (not_2_out, b4);
  and and_3 (and_3_out, not_2_out, s4);
  or or_1 (b___a, and_1_out, and_2_out, and_3_out);
endmodule

module ALU_5_Bits (
  input  [4:0] a,
  input  [4:0] b,
  input  [1:0] Op1,
  input  Op2,
  input  Op3,
  output [4:0] Resultado,
  output Sinal,
  output Overflow,
  output b___a,
  output a___b,
  output a___b_2,
  output Zero,
  output Carry
);

  wire overflow_flag_1_overflow;
  wire [4:0] logical_and_1_a___b, logical_or_1_a___b, multiplexer_2_out, n1_s_complement_1_complemento_de_1,
       n1_s_complement_2_complemento_de_1;
  wire [4:4] signal_flag_1_sinal;
  wire [5:0] full_adder_5_bits_1_soma, \full_subtractor_5_bits_1_diferença , multiplexer_1_out;

  Logical_AND logical_and_1 (.a___b(logical_and_1_a___b), .a(a), .b(b));
  Logical_OR logical_or_1 (.a___b(logical_or_1_a___b), .a(a), .b(b));
  _1_s_Complement u_1_s_complement_1 (.a(a), .Complemento_de_1(n1_s_complement_1_complemento_de_1));
  _1_s_Complement u_1_s_complement_2 (.a(b), .Complemento_de_1(n1_s_complement_2_complemento_de_1));
  Full_Adder_5_Bits full_adder_5_bits_1 (.Soma(full_adder_5_bits_1_soma), .a(a), .b(b));
  Full_Subtractor_5_Bits full_subtractor_5_bits_1 (.\Diferença (\full_subtractor_5_bits_1_diferença ), .a(a), .b(b));
  Multiplexer #(.width(6)) multiplexer_1 (
    .in0(full_adder_5_bits_1_soma), .in1(\full_subtractor_5_bits_1_diferença ), .out(multiplexer_1_out),
    .sel(Op2));
  Logic_Comparator_5_Bits logic_comparator_5_bits_1 (.a___b(a___b), .a(b), .b(a));
  Multiplexer #(.select(2), .width(5)) multiplexer_2 (
    .in0(logical_and_1_a___b), .in1(logical_or_1_a___b), .in2(n1_s_complement_1_complemento_de_1),
    .in3(n1_s_complement_2_complemento_de_1), .out(multiplexer_2_out), .sel(Op1));
  Signal_Flag signal_flag_1 (.Sinal(signal_flag_1_sinal[4]), .a4(a[4]), .b4(b[4]), .Op(Op2), .s4(multiplexer_1_out[4]));
  Overflow_Flag overflow_flag_1 (
    .Overflow(overflow_flag_1_overflow), .a4(a[4]), .b4(b[4]), .Op(Op2), .s4(multiplexer_1_out[4]));
  Aritmetic_Comparator_B aritmetic_comparator_b_1 (
    .b___a(b___a), .a4(a[4]), .s4(\full_subtractor_5_bits_1_diferença [5]), .b4(b[4]));
  Multiplexer #(.width(5)) multiplexer_3 (
    .in0(multiplexer_2_out), .in1({signal_flag_1_sinal[4], multiplexer_1_out[3:0]}), .out(Resultado),
    .sel(Op3));
  and and_1 (Carry, Op3, multiplexer_1_out[5]);
  and and_2 (Sinal, Op3, signal_flag_1_sinal[4]);
  and and_3 (Overflow, Op3, overflow_flag_1_overflow);
  nor nor_1 (a___b_2, b___a, a___b);
  nor nor_2 (Zero, Resultado[0], Resultado[1], Resultado[2], Resultado[3], Resultado[4], Carry);

  // Notes on the sheet:
  //   Op1 seleciona entre "AND Lógico", "OR Lógico"
  //   "Complemento de 1 de a" e "Complemento de 1 de b"
  //   Op2 seleciona entre "a+b" e "a-b"
  //   Op3 seleciona entre "Op1" e "Op2"
  //   Se "Op1" está selecionado, não há "Sinal" nem
  //   "Overflow" nem "Carry"
endmodule

module _1_s_Complement (
  input  [4:0] a,
  output [4:0] Complemento_de_1
);

  not not_1 (Complemento_de_1[0], a[0]);
  not not_2 (Complemento_de_1[1], a[1]);
  not not_3 (Complemento_de_1[2], a[2]);
  not not_4 (Complemento_de_1[3], a[3]);
  not not_5 (Complemento_de_1[4], a[4]);
endmodule

module Logical_AND (
  input  [4:0] a,
  input  [4:0] b,
  output [4:0] a___b
);

  and and_1 (a___b[0], a[0], b[0]);
  and and_2 (a___b[1], a[1], b[1]);
  and and_3 (a___b[2], a[2], b[2]);
  and and_4 (a___b[3], a[3], b[3]);
  and and_5 (a___b[4], a[4], b[4]);
endmodule

module Logical_OR (
  input  [4:0] a,
  input  [4:0] b,
  output [4:0] a___b
);

  or or_1 (a___b[0], a[0], b[0]);
  or or_2 (a___b[1], a[1], b[1]);
  or or_3 (a___b[2], a[2], b[2]);
  or or_4 (a___b[3], a[3], b[3]);
  or or_5 (a___b[4], a[4], b[4]);
endmodule
