// Logisim project guia6.circ as structural Verilog
module meia_soma_01 (
  input  e1,
  input  e2,
  output soma,
  output carry
);

  xor xor_1 (soma, e2, e1);
  and and_1 (carry, e1, e2);

  // Notes on the sheet:
  //   Isabella Gonçales - 420120
endmodule

module soma_completa_01 (
  input  e1,
  input  e2,
  input  e3,
  output carry_out,
  output soma
);

  wire meia_soma_01_1_carry, meia_soma_01_1_soma, meia_soma_01_2_carry;

  meia_soma_01 meia_soma_01_1 (.e1(e1), .e2(e2), .soma(meia_soma_01_1_soma), .carry(meia_soma_01_1_carry));
  meia_soma_01 meia_soma_01_2 (.e1(meia_soma_01_1_soma), .e2(e3), .soma(soma), .carry(meia_soma_01_2_carry));
  or or_1 (carry_out, meia_soma_01_1_carry, meia_soma_01_2_carry);

  // Notes on the sheet:
  //   Isabella Gonçales - 420120
endmodule

module Somador_5Bits_01 (
  input  [4:0] e1,
  input  [4:0] e2,
  output carry,
  output [4:0] somas
);

  wire meia_soma_01_1_carry, soma_completa_01_2_carry_out, soma_completa_01_3_carry_out,
       soma_completa_01_4_carry_out;

  soma_completa_01 soma_completa_01_1 (
    .e1(e1[4]), .e2(e2[4]), .e3(soma_completa_01_2_carry_out), .carry_out(carry), .soma(somas[4]));
  soma_completa_01 soma_completa_01_2 (
    .e1(e1[3]), .e2(e2[3]), .e3(soma_completa_01_3_carry_out), .carry_out(soma_completa_01_2_carry_out),
    .soma(somas[3]));
  soma_completa_01 soma_completa_01_3 (
    .e1(e1[2]), .e2(e2[2]), .e3(soma_completa_01_4_carry_out), .carry_out(soma_completa_01_3_carry_out),
    .soma(somas[2]));
  soma_completa_01 soma_completa_01_4 (
    .e1(e1[1]), .e2(e2[1]), .e3(meia_soma_01_1_carry), .carry_out(soma_completa_01_4_carry_out),
    .soma(somas[1]));
  meia_soma_01 meia_soma_01_1 (.e1(e1[0]), .e2(e2[0]), .soma(somas[0]), .carry(meia_soma_01_1_carry));

  // Notes on the sheet:
  //   Isabella Gonçales - 420120 
endmodule

module Comparador_01 (
  input  [4:0] e1,
  input  [4:0] e2,
  output comparador
);

  ExactlyOne xor_1 (
    .out(comparador), .in0(e1[0]), .in1(e1[1]), .in2(e1[2]), .in3(e1[3]), .in4(e1[4]), .in5(e2[0]),
    .in6(e2[1]), .in7(e2[2]), .in8(e2[3]), .in9(e2[4]));

  // Notes on the sheet:
  //   Isabella Gonçales - 420120
endmodule

module ALU_5_Bits_01 (
  input  [4:0] e1,
  input  [4:0] e2,
  input  chave,
  output [4:0] out_4
);

  wire [4:0] comparador_01_1_comparador, somador_5bits_01_1_somas;

  Somador_5Bits_01 somador_5bits_01_1 (.e1(e1), .e2(e2), .somas(somador_5bits_01_1_somas));  // open: carry
  Comparador_01 comparador_01_1 (.e1(e1), .e2(e2), .comparador(comparador_01_1_comparador[0]));
  Multiplexer #(.width(5)) multiplexer_1 (
    .in0(somador_5bits_01_1_somas), .in1(comparador_01_1_comparador), .out(out_4), .sel(chave));

  // Notes on the sheet:
  //   Isabella Gonçales - 420120
endmodule

module \meia_diferença_02  (
  input  e1,
  input  e2,
  output \diferença ,
  output sinal
);

  wire not_1_out;

  xor xor_1 (\diferença , e1, e2);
  not not_1 (not_1_out, e1);
  and and_1 (sinal, e2, not_1_out);

  // Notes on the sheet:
  //   Isabella Gonçales - 420120
endmodule

module \diferença_completa_02  (
  input  e1,
  input  e2,
  input  e3,
  output sinal,
  output \diferença 
);

  wire \meia_diferença_02_1_diferença , \meia_diferença_02_1_sinal , \meia_diferença_02_2_sinal ;

  \meia_diferença_02  \meia_diferença_02_1  (
    .e1(e1), .e2(e2), .\diferença (\meia_diferença_02_1_diferença ), .sinal(\meia_diferença_02_1_sinal ));
  \meia_diferença_02  \meia_diferença_02_2  (
    .e1(\meia_diferença_02_1_diferença ), .e2(e3), .\diferença (\diferença ),
    .sinal(\meia_diferença_02_2_sinal ));
  or or_1 (sinal, \meia_diferença_02_1_sinal , \meia_diferença_02_2_sinal );

  // Notes on the sheet:
  //   temp1
  //   temp2
  //   Isabella Gonçales - 420120
  //   temp3
endmodule

module \Diferença_5Bits  (
  input  [4:0] e1,
  input  [4:0] e2,
  output out_3,
  output [4:0] \Diferenças 
);

  wire \diferença_completa_02_2_sinal , \diferença_completa_02_3_sinal , \diferença_completa_02_4_sinal ,
       \meia_diferença_02_1_sinal ;

  \diferença_completa_02  \diferença_completa_02_1  (
    .e1(e1[4]), .e2(e2[4]), .e3(\diferença_completa_02_2_sinal ), .sinal(out_3), .\diferença (\Diferenças [4]));
  \diferença_completa_02  \diferença_completa_02_2  (
    .e1(e1[3]), .e2(e2[3]), .e3(\diferença_completa_02_3_sinal ), .sinal(\diferença_completa_02_2_sinal ),
    .\diferença (\Diferenças [3]));
  \diferença_completa_02  \diferença_completa_02_3  (
    .e1(e1[2]), .e2(e2[2]), .e3(\diferença_completa_02_4_sinal ), .sinal(\diferença_completa_02_3_sinal ),
    .\diferença (\Diferenças [2]));
  \diferença_completa_02  \diferença_completa_02_4  (
    .e1(e1[1]), .e2(e2[1]), .e3(\meia_diferença_02_1_sinal ), .sinal(\diferença_completa_02_4_sinal ),
    .\diferença (\Diferenças [1]));
  \meia_diferença_02  \meia_diferença_02_1  (
    .e1(e1[0]), .e2(e2[0]), .\diferença (\Diferenças [0]), .sinal(\meia_diferença_02_1_sinal ));

  // Notes on the sheet:
  //   Isabella Gonçales - 420120
endmodule
