// Logisim project guia6.circ as structural Verilog: 5 circuits, main circuit main
module main (
  input  a1,
  input  b1,
  input  a2,
  input  b2,
  input  a3,
  input  b3,
  output s1,
  output s2,
  output s3
);

  wire diferenca_completa_1_s1, meia_diferenca_1_s1;

  meia_diferenca meia_diferenca_1 (.x(a1), .y(b1), .s0(s1), .s1(meia_diferenca_1_s1));
  diferenca_completa diferenca_completa_1 (
    .e1(meia_diferenca_1_s1), .x(a2), .y(b2), .s0(s2), .s1(diferenca_completa_1_s1));
  diferenca_completa diferenca_completa_2 (.e1(diferenca_completa_1_s1), .x(a3), .y(b3), .s0(s3));  // open: s1

  // Notes on the sheet:
  //   Karen Alves - 407451
  //   Diferenca Comple com 3 bits
  //   C1
  //   C2
endmodule

module meia_diferenca (
  input  x,
  input  y,
  output s0,
  output s1
);

  wire not_1_out;

  not not_1 (not_1_out, x);
  xor s (s0, x, y);
  and a (s1, not_1_out, y);

  // Notes on the sheet:
  //   Meia diferenca
  //   Karen Alves - 407451
endmodule

module diferenca_completa (
  input  e1,
  input  x,
  input  y,
  output s0,
  output s1
);

  wire a_out, not_1_out, not_2_out, s_out, v2_out;

  xor s (s_out, x, y);
  not not_1 (not_1_out, x);
  and a (a_out, not_1_out, y);
  not not_2 (not_2_out, s_out);
  xor u_s0 (s0, e1, s_out);
  and v2 (v2_out, e1, not_2_out);
  or u_s1 (s1, v2_out, a_out);

  // Notes on the sheet:
  //   Karen Alves - 407451
  //   Diferenca completa
endmodule

module diferenca_completa5bit (
  input  a1,
  input  b1,
  input  a2,
  input  b2,
  input  a3,
  input  b3,
  input  a4,
  input  b4,
  input  a5,
  input  b5,
  output s1,
  output s2,
  output s3,
  output s4,
  output s5,
  output cout
);

  wire diferenca_completa_1_s1, diferenca_completa_2_s1, diferenca_completa_3_s1, meia_diferenca_1_s1;

  meia_diferenca meia_diferenca_1 (.x(a1), .y(b1), .s0(s1), .s1(meia_diferenca_1_s1));
  diferenca_completa diferenca_completa_1 (
    .e1(meia_diferenca_1_s1), .x(a2), .y(b2), .s0(s2), .s1(diferenca_completa_1_s1));
  diferenca_completa diferenca_completa_2 (
    .e1(diferenca_completa_1_s1), .x(a3), .y(b3), .s0(s3), .s1(diferenca_completa_2_s1));
  diferenca_completa diferenca_completa_3 (
    .e1(diferenca_completa_2_s1), .x(a4), .y(b4), .s0(s4), .s1(diferenca_completa_3_s1));
  diferenca_completa diferenca_completa_4 (.e1(diferenca_completa_3_s1), .x(a5), .y(b5), .s0(s5), .s1(cout));

  // Notes on the sheet:
  //   C2
  //   C1
  //   Karen Alves - 407451
endmodule

module ALU (
  input  a1,
  input  a2,
  input  a3,
  input  a4,
  input  a5,
  input  b1,
  input  b2,
  input  b3,
  input  b4,
  input  b5,
  output [4:0] out_11
);

  // diferenca_completa5bit diferenca_completa5bit_1: pin names not known; wires that end beside it: a1, a2, a3, a4, a5, b1, b2, b3, b4, b5, out_11, out_11, out_11, out_11, out_11, out_11

  // Notes on the sheet:
  //   Karen Alves - 407451
endmodule
