// Logisim project Simulaçoes Guia 06.circ as structural Verilog: 19 circuits, main circuit meia-soma
module meia_somaNAND (
  input  a,
  input  b,
  output s0,
  output s1
);

  wire temp1_out, temp2_out, temp3_out, temp4_out;

  nand temp1 (temp1_out, a, b);
  nand temp4 (temp4_out, b, a);
  nand temp2 (temp2_out, a, temp1_out);
  nand temp3 (temp3_out, temp1_out, b);
  nand temp5 (s0, temp4_out, temp4_out);
  nand temp4_2 (s1, temp2_out, temp3_out);

  // Notes on the sheet:
  //   Silvino Henrique Santos de Souza - 412773
  //   Circuito Meia - Soma usando Somente NANDs
  //   temp5 = s0
  //   temp 4 = s1
endmodule

module meia_soma (
  input  a,
  input  b,
  output s0,
  output s1
);

  and and_1 (s0, b, a);
  xor xor_1 (s1, a, b);

  // Notes on the sheet:
  //   Silvino Henrique Santos de Souza - 412773
  //   Meia -Soma Compacto
endmodule

module Somador_Completo (
  input  a,
  input  b,
  input  Cin,
  output Cout,
  output Soma
);

  wire meia_soma_1_s0, meia_soma_1_s1, meia_soma_2_s0;

  or or_1 (Cout, meia_soma_1_s0, meia_soma_2_s0);
  meia_soma meia_soma_1 (.a(a), .b(b), .s0(meia_soma_1_s0), .s1(meia_soma_1_s1));
  meia_soma meia_soma_2 (.a(meia_soma_1_s1), .b(Cin), .s0(meia_soma_2_s0), .s1(Soma));

  // Notes on the sheet:
  //   Silvino Henrique Santos de Souza - 412773
  //   Somador Completo 
endmodule

module Somador_Completo2 (
  input  a,
  input  b,
  input  Cin,
  output Cout,
  output Soma
);

  wire meia_somanand_1_s0, meia_somanand_1_s1, meia_somanand_2_s0;

  meia_somaNAND meia_somanand_1 (.a(a), .b(b), .s0(meia_somanand_1_s0), .s1(meia_somanand_1_s1));
  or or_1 (Cout, meia_somanand_1_s0, meia_somanand_2_s0);
  meia_somaNAND meia_somanand_2 (.a(meia_somanand_1_s1), .b(Cin), .s0(meia_somanand_2_s0), .s1(Soma));

  // Notes on the sheet:
  //   Somador Completo (subcircuito com NANDs)
  //   Silvino Henrique Santos de Souza - 412773
endmodule

module Somador_Completo3bits (
  input  b2,
  input  a2,
  input  b1,
  input  a1,
  input  b0,
  input  a0,
  output Cout,
  output s20,
  output s10,
  output s00
);

  wire meia_somanand_1_s0, somador_completo2_2_cout;

  Somador_Completo2 somador_completo2_1 (.a(a2), .b(b2), .Cin(somador_completo2_2_cout), .Cout(Cout), .Soma(s20));
  Somador_Completo2 somador_completo2_2 (
    .a(a1), .b(b1), .Cin(meia_somanand_1_s0), .Cout(somador_completo2_2_cout), .Soma(s10));
  meia_somaNAND meia_somanand_1 (.a(a0), .b(b0), .s0(meia_somanand_1_s0), .s1(s00));

  // Notes on the sheet:
  //   Somador de 3Bits(com NAND's)
  //   Guia05 - 04
  //   Silvino Henrique Santos de Souza - 412773
endmodule

module Somador_Completo4bits (
  input  b3,
  input  a3,
  input  b2,
  input  a2,
  input  b1,
  input  a1,
  input  b0,
  input  a0,
  output Cout,
  output s30,
  output s20,
  output s10,
  output s00
);

  wire meia_soma_1_s0, somador_completo_2_cout, somador_completo_3_cout;

  Somador_Completo somador_completo_1 (.a(a3), .b(b3), .Cin(somador_completo_2_cout), .Cout(Cout), .Soma(s30));
  Somador_Completo somador_completo_2 (
    .a(a2), .b(b2), .Cin(somador_completo_3_cout), .Cout(somador_completo_2_cout), .Soma(s20));
  Somador_Completo somador_completo_3 (
    .a(a1), .b(b1), .Cin(meia_soma_1_s0), .Cout(somador_completo_3_cout), .Soma(s10));
  meia_soma meia_soma_1 (.a(a0), .b(b0), .s0(meia_soma_1_s0), .s1(s00));

  // Notes on the sheet:
  //   Somador de 4Bits
  //   Guia05 - 01
  //   Silvino Henrique Santos de Souza - 412773
endmodule

module Somador_Completo5bits (
  input  b4,
  input  a4,
  input  b3,
  input  a3,
  input  b2,
  input  a2,
  input  b1,
  input  a1,
  input  b0,
  input  a0,
  output Cout,
  output s40,
  output s30,
  output s20,
  output s10,
  output s00
);

  wire meia_soma_1_s0, somador_completo_2_cout, somador_completo_3_cout, somador_completo_4_cout;

  Somador_Completo somador_completo_1 (.a(a4), .b(b4), .Cin(somador_completo_2_cout), .Cout(Cout), .Soma(s40));
  Somador_Completo somador_completo_2 (
    .a(a3), .b(b3), .Cin(somador_completo_3_cout), .Cout(somador_completo_2_cout), .Soma(s30));
  Somador_Completo somador_completo_3 (
    .a(a2), .b(b2), .Cin(somador_completo_4_cout), .Cout(somador_completo_3_cout), .Soma(s20));
  Somador_Completo somador_completo_4 (
    .a(a1), .b(b1), .Cin(meia_soma_1_s0), .Cout(somador_completo_4_cout), .Soma(s10));
  meia_soma meia_soma_1 (.a(a0), .b(b0), .s0(meia_soma_1_s0), .s1(s00));

  // Notes on the sheet:
  //   Somador de 5Bits
  //   Guia06 - 01
  //   Silvino Henrique Santos de Souza - 412773
endmodule

module \meia_diferençaNOR  (
  input  a,
  input  b,
  output s0,
  output s1
);

  wire temp1_out, temp2_out, temp3_out, temp4_out, temp5_out, temp6_out, temp7_out;

  nor temp5 (temp5_out, a, a);
  nor temp1 (temp1_out, a, b);
  nor temp2 (temp2_out, a, temp1_out);
  nor temp3 (temp3_out, temp1_out, b);
  nor temp6 (temp6_out, temp5_out, temp5_out);
  nor temp7 (temp7_out, b, b);
  nor temp4 (temp4_out, temp2_out, temp3_out);
  nor nor_1 (s0, temp6_out, temp7_out);
  nor nor_2 (s1, temp4_out, temp4_out);

  // Notes on the sheet:
  //   Meia-Diferença somente com NORs
  //   Silvino Henrique Santos de Souza - 412773
endmodule

module \meia_diferença  (
  input  a,
  input  b,
  output s0,
  output s1
);

  wire not_1_out;

  and and_1 (s0, b, not_1_out);
  not not_1 (not_1_out, a);
  xor xor_1 (s1, a, b);

  // Notes on the sheet:
  //   Silvino Henrique Santos de Souza - 412773
  //   Meia - Diferença Compacto
endmodule

module \meia_diferençaNAND  (
  input  a,
  input  b,
  output s0,
  output s1
);

  wire temp1_out, temp2_out, temp3_out, temp4_out, temp5_out;

  nand temp4 (temp4_out, a, a);
  nand temp1 (temp1_out, a, b);
  nand temp5 (temp5_out, b, temp4_out);
  nand temp2 (temp2_out, a, temp1_out);
  nand temp3 (temp3_out, temp1_out, b);
  nand nand_1 (s0, temp5_out, temp5_out);
  nand nand_2 (s1, temp2_out, temp3_out);

  // Notes on the sheet:
  //   Circuito Meia - Diferença usando Somente NANDs
  //   Silvino Henrique Santos de Souza - 412773
endmodule

module Subtrator_Completo (
  input  a,
  input  b,
  input  Cin,
  output Cout,
  output \Diferença 
);

  wire \meia_diferença_1_s0 , \meia_diferença_1_s1 , \meia_diferença_2_s0 ;

  or or_1 (Cout, \meia_diferença_1_s0 , \meia_diferença_2_s0 );
  \meia_diferença  \meia_diferença_1  (.a(a), .b(b), .s0(\meia_diferença_1_s0 ), .s1(\meia_diferença_1_s1 ));
  \meia_diferença  \meia_diferença_2  (
    .a(\meia_diferença_1_s1 ), .b(Cin), .s0(\meia_diferença_2_s0 ), .s1(\Diferença ));

  // Notes on the sheet:
  //   Cin: pull=down
  //   Silvino Henrique Santos de Souza - 412773
  //   Subtrator Completo 
endmodule

module Subtrator_Completo2 (
  input  a,
  input  b,
  input  Cin,
  output Cout,
  output \Diferença 
);

  wire \meia_diferençanand_1_s0 , \meia_diferençanand_1_s1 , \meia_diferençanand_2_s0 ;

  \meia_diferençaNAND  \meia_diferençanand_1  (
    .a(a), .b(b), .s0(\meia_diferençanand_1_s0 ), .s1(\meia_diferençanand_1_s1 ));
  or or_1 (Cout, \meia_diferençanand_1_s0 , \meia_diferençanand_2_s0 );
  \meia_diferençaNAND  \meia_diferençanand_2  (
    .a(\meia_diferençanand_1_s1 ), .b(Cin), .s0(\meia_diferençanand_2_s0 ), .s1(\Diferença ));

  // Notes on the sheet:
  //   Cin: pull=down
  //   Subtrator Completo (subcircuito com NANDs)
  //   Silvino Henrique Santos de Souza - 412773
endmodule

module Subtrator_Completo3 (
  input  a,
  input  b,
  input  Cin,
  output Cout,
  output \Diferença 
);

  wire \meia_diferençanor_1_s0 , \meia_diferençanor_2_s0 , \meia_diferençanor_2_s1 ;

  or or_1 (Cout, \meia_diferençanor_2_s0 , \meia_diferençanor_1_s0 );
  \meia_diferençaNOR  \meia_diferençanor_1  (
    .a(\meia_diferençanor_2_s1 ), .b(Cin), .s0(\meia_diferençanor_1_s0 ), .s1(\Diferença ));
  \meia_diferençaNOR  \meia_diferençanor_2  (
    .a(a), .b(b), .s0(\meia_diferençanor_2_s0 ), .s1(\meia_diferençanor_2_s1 ));

  // Notes on the sheet:
  //   Cin: pull=down
  //   Subtrator Completo (subcircuito com NORs)
  //   Silvino Henrique Santos de Souza - 412773
endmodule

module Subtrator_Completo3bits (
  input  b2,
  input  a2,
  input  b1,
  input  a1,
  input  b0,
  input  a0,
  output Cout,
  output s20,
  output s10,
  output s00
);

  wire \meia_diferença_1_s0 , subtrator_completo_2_cout;

  Subtrator_Completo subtrator_completo_1 (
    .a(a2), .b(b2), .Cin(subtrator_completo_2_cout), .Cout(Cout), .\Diferença (s20));
  Subtrator_Completo subtrator_completo_2 (
    .a(a1), .b(b1), .Cin(\meia_diferença_1_s0 ), .Cout(subtrator_completo_2_cout), .\Diferença (s10));
  \meia_diferença  \meia_diferença_1  (.a(a0), .b(b0), .s0(\meia_diferença_1_s0 ), .s1(s00));

  // Notes on the sheet:
  //   Subtrator de 3Bits
  //   Guia05 - 02
  //   Silvino Henrique Santos de Souza - 412773
endmodule

module Subtrator_Completo3bitsNOR (
  input  b2,
  input  a2,
  input  b1,
  input  a1,
  input  b0,
  input  a0,
  output Cout,
  output s20,
  output s10,
  output s00
);

  wire \meia_diferençanor_1_s0 , subtrator_completo3_2_cout;

  Subtrator_Completo3 subtrator_completo3_1 (
    .a(a2), .b(b2), .Cin(subtrator_completo3_2_cout), .Cout(Cout), .\Diferença (s20));
  Subtrator_Completo3 subtrator_completo3_2 (
    .a(a1), .b(b1), .Cin(\meia_diferençanor_1_s0 ), .Cout(subtrator_completo3_2_cout), .\Diferença (s10));
  \meia_diferençaNOR  \meia_diferençanor_1  (.a(a0), .b(b0), .s0(\meia_diferençanor_1_s0 ), .s1(s00));

  // Notes on the sheet:
  //   Subtrator de 3Bits
  //   Guia05 - 05
  //   Silvino Henrique Santos de Souza - 412773
endmodule

module Subtrator_Completo5bits (
  input  b4,
  input  a4,
  input  b3,
  input  a3,
  input  b2,
  input  a2,
  input  b1,
  input  a1,
  input  b0,
  input  a0,
  output Cout,
  output s40,
  output s30,
  output s20,
  output s10,
  output s00
);

  wire \meia_diferença_1_s0 , subtrator_completo_2_cout, subtrator_completo_3_cout, subtrator_completo_4_cout;

  Subtrator_Completo subtrator_completo_1 (
    .a(a4), .b(b4), .Cin(subtrator_completo_2_cout), .Cout(Cout), .\Diferença (s40));
  Subtrator_Completo subtrator_completo_2 (
    .a(a3), .b(b3), .Cin(subtrator_completo_3_cout), .Cout(subtrator_completo_2_cout), .\Diferença (s30));
  Subtrator_Completo subtrator_completo_3 (
    .a(a2), .b(b2), .Cin(subtrator_completo_4_cout), .Cout(subtrator_completo_3_cout), .\Diferença (s20));
  Subtrator_Completo subtrator_completo_4 (
    .a(a1), .b(b1), .Cin(\meia_diferença_1_s0 ), .Cout(subtrator_completo_4_cout), .\Diferença (s10));
  \meia_diferença  \meia_diferença_1  (.a(a0), .b(b0), .s0(\meia_diferença_1_s0 ), .s1(s00));

  // Notes on the sheet:
  //   Subtrator de 5Bits
  //   Guia06 - 02
  //   Silvino Henrique Santos de Souza - 412773
endmodule

module Produto_Completo3bits (
  input  a0,
  input  in_2,
  input  b0,
  input  a1,
  input  b0_2,
  input  a0_2,
  input  b1,
  input  a2,
  input  b0_3,
  input  a1_2,
  input  b1_2,
  input  a0_3,
  input  b2,
  input  a2_2,
  input  b1_3,
  input  a1_3,
  input  b2_2,
  input  a2_3,
  input  b2_3,
  output s10,
  output s20,
  output s30,
  output s40,
  output s50,
  output Cout
);

  wire and_1_out, and_2_out, and_3_out, and_4_out, and_5_out, and_6_out, and_7_out, and_8_out, and_9_out,
       meia_soma_1_s1, meia_soma_2_s0, somador_completo_1_cout, somador_completo_2_soma,
       somador_completo_3_cout;

  and and_1 (and_1_out, a0, b0);
  and and_2 (and_2_out, a1, b0_2);
  and and_3 (and_3_out, a0_2, b1);
  and and_4 (and_4_out, a2, b0_3);
  and and_5 (and_5_out, a1_2, b1_2);
  and and_6 (and_6_out, a0_3, b2);
  and and_7 (and_7_out, a2_2, b1_3);
  and and_8 (and_8_out, a1_3, b2_2);
  and and_9 (and_9_out, a2_3, b2_3);
  meia_soma meia_soma_1 (.a(and_1_out), .b(in_2), .s0(s10), .s1(meia_soma_1_s1));
  Somador_Completo somador_completo_1 (
    .a(and_2_out), .b(and_3_out), .Cin(meia_soma_1_s1), .Cout(somador_completo_1_cout), .Soma(s20));
  Somador_Completo somador_completo_2 (
    .a(and_4_out), .b(and_5_out), .Cin(and_6_out), .Soma(somador_completo_2_soma));  // open: Cout
  meia_soma meia_soma_2 (.a(somador_completo_1_cout), .b(somador_completo_2_soma), .s0(meia_soma_2_s0), .s1(s30));
  Somador_Completo somador_completo_3 (
    .a(and_7_out), .b(and_8_out), .Cin(meia_soma_2_s0), .Cout(somador_completo_3_cout), .Soma(s40));
  meia_soma meia_soma_3 (.a(and_9_out), .b(somador_completo_3_cout), .s0(Cout), .s1(s50));

  // Notes on the sheet:
  //   Guia05 - 03
  //   temp10
  //   temp11
  //   temp12
  //   temp14
  //   Produto-completo 3 bits
  //   temp13
  //   Silvino Henrique Santos de Souza - 412773
endmodule

module ALU (
  input  a0,
  input  a1,
  input  a2,
  input  a3,
  input  a4,
  input  b0,
  input  b1,
  input  b2,
  input  b3,
  input  b4,
  output [4:0] resultado,
  output Cout
);

  Somador_Completo5bits somador_completo5bits_1 (
    .Cout(Cout), .b4(b4), .a4(a4), .b3(b3), .a3(a3), .b2(b2), .a2(a2), .b1(b1), .a1(a1), .b0(b0), .a0(a0),
    .s40(resultado[4]), .s30(resultado[3]), .s20(resultado[2]), .s10(resultado[1]), .s00(resultado[0]));

  // Notes on the sheet:
  //   Somador de 5Bits
  //   Guia06 - 01
  //   Silvino Henrique Santos de Souza - 412773
endmodule

module ALU2 (
  input  [4:0] a,
  input  [4:0] in_2,
  input  [4:0] b,
  output Cout
);

  Subtrator_Completo5bits subtrator_completo5bits_1 (
    .Cout(Cout), .b4(b[4]), .a4(a[4]), .b3(b[3]), .a3(a[3]), .b2(b[2]), .a2(a[2]), .b1(b[1]), .a1(a[1]),
    .b0(b[0]), .a0(a[0]), .s40(in_2[4]), .s30(in_2[3]), .s20(in_2[2]), .s10(in_2[1]), .s00(in_2[0]));

  // Notes on the sheet:
  //   Subtrator de 5Bits
  //   Guia06 - 02
  //   Silvino Henrique Santos de Souza - 412773
endmodule
