// Logisim project somador com comparador Logico.circ as structural Verilog: 4 circuits, main circuit main
module main (
  input  x,
  input  y,
  output Vout,
  output s
);

  and and_1 (Vout, y, x);
  xor xor_1 (s, x, y);
endmodule

module HA (
  input  x,
  input  y,
  input  Vin,
  output Vout,
  output s
);

  wire main_1_s, main_1_vout, main_2_vout;

  or or_1 (Vout, main_1_vout, main_2_vout);
  main main_1 (.Vout(main_1_vout), .x(x), .y(y), .s(main_1_s));
  main main_2 (.Vout(main_2_vout), .x(Vin), .y(main_1_s), .s(s));
endmodule

module FA (
  input  a3,
  input  b3,
  input  a2,
  input  b2,
  input  a1,
  input  b1,
  input  a0,
  input  b0,
  output Vout,
  output s3,
  output s2,
  output s1,
  output s0
);

  wire ha_2_vout, ha_3_vout, main_1_vout;

  HA ha_1 (.Vout(Vout), .x(a3), .y(b3), .s(s3), .Vin(ha_2_vout));
  HA ha_2 (.Vout(ha_2_vout), .x(a2), .y(b2), .s(s2), .Vin(ha_3_vout));
  HA ha_3 (.Vout(ha_3_vout), .x(a1), .y(b1), .s(s1), .Vin(main_1_vout));
  main main_1 (.Vout(main_1_vout), .x(a0), .y(b0), .s(s0));
endmodule

module FA4b (
  input  [3:0] a,
  input  [3:0] b,
  output Cout,
  output s3,
  output s2,
  output s1,
  output s0,
  output out_8
);

  wire xnor_1_out, xnor_2_out, xnor_3_out, xnor_4_out;

  FA fa_1 (
    .Vout(Cout), .a3(a[3]), .b3(b[3]), .a2(a[2]), .b2(b[2]), .a1(a[1]), .b1(b[1]), .a0(a[0]), .b0(b[0]),
    .s3(s3), .s2(s2), .s1(s1), .s0(s0));
  xnor xnor_1 (xnor_1_out, b[3], a[3]);
  xnor xnor_2 (xnor_2_out, b[2], a[2]);
  and and_1 (out_8, xnor_1_out, xnor_2_out, xnor_3_out, xnor_4_out);
  xnor xnor_3 (xnor_3_out, b[1], a[1]);
  xnor xnor_4 (xnor_4_out, b[0], a[0]);

  // Notes on the sheet:
  //   1 => a = b
  //   0 => a != b
endmodule
