// Logisim project somador subtrator comparador logico, comparador aritmetico, detector e compl de 1.circ as structural Verilog: 4 circuits, main circuit main
module main (
  input  x,
  input  y,
  output Vout,
  output s
);

  and and_1 (Vout, y, x);
  xor xor_1 (s, x, y);
endmodule

module Ha (
  input  x,
  input  y,
  input  Vin,
  output Vout,
  output s
);

  wire main_1_s, main_1_vout, main_2_vout;

  or or_1 (Vout, main_1_vout, main_2_vout);
  main main_1 (.Vout(main_1_vout), .x(x), .y(y), .s(main_1_s));
  main main_2 (.Vout(main_2_vout), .x(Vin), .y(main_1_s), .s(s));
endmodule

module Fa (
  input  a3,
  input  b3,
  input  a2,
  input  b2,
  input  a1,
  input  b1,
  input  a0,
  input  b0,
  input  Vin,
  output Vout,
  output s3,
  output s2,
  output s1,
  output s0
);

  wire ha_1_vout, ha_3_vout, ha_4_vout;

  Ha ha_1 (.Vout(ha_1_vout), .x(a2), .y(b2), .s(s2), .Vin(ha_3_vout));
  Ha ha_2 (.Vout(Vout), .x(a3), .y(b3), .s(s3), .Vin(ha_1_vout));
  Ha ha_3 (.Vout(ha_3_vout), .x(a1), .y(b1), .s(s1), .Vin(ha_4_vout));
  Ha ha_4 (.Vout(ha_4_vout), .x(a0), .y(b0), .s(s0), .Vin(Vin));
endmodule

module FA4B (
  input  [3:0] a,
  input  [3:0] b,
  input  Sel,
  output Cout,
  output out_5,
  output _1____a___b,
  output _1____a___b_2,
  output s3,
  output s2,
  output s1,
  output s0,
  output s3_2,
  output s2_2,
  output s1_2,
  output s0_2,
  output detector
);

  wire and_3_out, and_4_out, and_5_out, and_6_out, and_7_out, and_8_out, and_9_out, and_10_out, not_1_out,
       not_6_out, not_7_out, not_8_out, not_9_out, not_10_out, not_11_out, not_12_out, not_13_out,
       xnor_1_out, xnor_2_out, xnor_3_out, xnor_4_out, xor_1_out, xor_2_out, xor_3_out, xor_4_out;

  xor xor_1 (xor_1_out, Sel, b[3]);
  not not_1 (not_1_out, Cout);
  and and_1 (detector, Sel, not_1_out);
  not not_2 (s3_2, s3);
  xor xor_2 (xor_2_out, Sel, b[2]);
  Fa fa_1 (
    .Vout(Cout), .a3(a[3]), .b3(xor_1_out), .a2(a[2]), .b2(xor_2_out), .a1(a[1]), .b1(xor_3_out), .a0(a[0]),
    .b0(xor_4_out), .s3(s3), .s2(s2), .s1(s1), .s0(s0), .Vin(Sel));
  not not_3 (s2_2, s2);
  not not_4 (s1_2, s1);
  not not_5 (s0_2, s0);
  xor xor_3 (xor_3_out, Sel, b[1]);
  xor xor_4 (xor_4_out, Sel, b[0]);
  xnor xnor_1 (xnor_1_out, b[3], a[3]);
  xnor xnor_2 (xnor_2_out, b[2], a[2]);
  xnor xnor_3 (xnor_3_out, b[1], a[1]);
  and and_2 (out_5, xnor_1_out, xnor_2_out, xnor_3_out, xnor_4_out);
  xnor xnor_4 (xnor_4_out, b[0], a[0]);
  not not_6 (not_6_out, a[3]);
  and and_3 (and_3_out, b[3], not_6_out);
  not not_7 (not_7_out, a[2]);
  and and_4 (and_4_out, b[2], xnor_1_out, not_7_out);
  or or_1 (_1____a___b, and_3_out, and_4_out, and_5_out, and_6_out);
  not not_8 (not_8_out, a[1]);
  and and_5 (and_5_out, b[1], xnor_1_out, xnor_2_out, not_8_out);
  not not_9 (not_9_out, a[0]);
  and and_6 (and_6_out, b[0], xnor_1_out, xnor_2_out, xnor_3_out, not_9_out);
  not not_10 (not_10_out, b[3]);
  and and_7 (and_7_out, not_10_out, a[3]);
  not not_11 (not_11_out, b[2]);
  and and_8 (and_8_out, not_11_out, xnor_1_out, a[2]);
  not not_12 (not_12_out, b[1]);
  and and_9 (and_9_out, not_12_out, xnor_1_out, xnor_2_out, a[1]);
  or or_2 (_1____a___b_2, and_7_out, and_8_out, and_9_out, and_10_out);
  not not_13 (not_13_out, b[0]);
  and and_10 (and_10_out, not_13_out, xnor_3_out, xnor_2_out, xnor_1_out, a[0]);

  // Notes on the sheet:
  //   0 = soma
  //   1 = subtração
  //   0 = resultado negativo
  //   1 = resultado positivo ou 0
  //   o detector so habilita se for subtração = > sel = 1
  //   calcula o complemento de 1
  //   1 => a = b
  //   0 => a != b
  //   comparador logico
  //   comparadores aritmeticos
endmodule
