// Logisim project Guia 07.circ as structural Verilog: 16 circuits, main circuit MeiaSoma
module MeiaSoma (
  input  a,
  input  b,
  output s,
  output COut
);

  xor xor_1 (s, a, b);
  and and_1 (COut, a, b);

  // Notes on the sheet:
  //   Bruno César Lopes Silva - 415985
endmodule

module SomaCompleta (
  input  a,
  input  b,
  input  vaium,
  output s,
  output COut
);

  wire meiasoma_1_cout, meiasoma_1_s, meiasoma_2_cout;

  MeiaSoma meiasoma_1 (.a(a), .b(b), .s(meiasoma_1_s), .COut(meiasoma_1_cout));
  MeiaSoma meiasoma_2 (.a(meiasoma_1_s), .b(vaium), .s(s), .COut(meiasoma_2_cout));
  or or_1 (COut, meiasoma_2_cout, meiasoma_1_cout);

  // Notes on the sheet:
  //   Bruno César Lopes Silva - 415985
endmodule

module Somador (
  input  [3:0] b,
  input  [3:0] a,
  output Overflow,
  output CarryOut,
  output [3:0] s
);

  wire meiasoma_1_cout, somacompleta_2_cout, somacompleta_3_cout;

  xor xor_1 (Overflow, CarryOut, somacompleta_2_cout);
  SomaCompleta somacompleta_1 (.a(a[3]), .b(b[3]), .vaium(somacompleta_2_cout), .s(s[3]), .COut(CarryOut));
  SomaCompleta somacompleta_2 (.a(a[2]), .b(b[2]), .vaium(somacompleta_3_cout), .s(s[2]), .COut(somacompleta_2_cout));
  SomaCompleta somacompleta_3 (.a(a[1]), .b(b[1]), .vaium(meiasoma_1_cout), .s(s[1]), .COut(somacompleta_3_cout));
  MeiaSoma meiasoma_1 (.a(a[0]), .b(b[0]), .s(s[0]), .COut(meiasoma_1_cout));

  // Notes on the sheet:
  //   Bruno César Lopes Silva - 415985
endmodule

module Comparador (
  input  [3:0] b,
  input  [3:0] a,
  output s
);

  wire [3:0] xnor_1_out;

  assign xnor_1_out = ~(b ^ a);  // XNOR_Gate xnor_1, 4 bits wide
  and and_1 (s, xnor_1_out[3], xnor_1_out[2], xnor_1_out[1], xnor_1_out[0]);

  // Notes on the sheet:
  //   Bruno César Lopes Silva - 415985
endmodule

module ALU (
  input  [3:0] b,
  input  [3:0] a,
  output comparador,
  output OVF,
  output COut,
  output [3:0] s
);

  Comparador comparador_1 (.b(b), .a(a), .s(comparador));
  Somador somador_1 (.b(b), .a(a), .Overflow(OVF), .CarryOut(COut), .s(s));

  // Notes on the sheet:
  //   Bruno César Lopes Silva - 415985
  //   1 - Iguais
  //   0 - Diferentes
endmodule

module MeiaDiferenca (
  input  a,
  input  b,
  output s,
  output vemum
);

  wire not_1_out;

  not not_1 (not_1_out, a);
  xor xor_1 (s, a, b);
  and and_1 (vemum, not_1_out, b);

  // Notes on the sheet:
  //   Bruno César Lopes Silva - 415985
endmodule

module DiferencaCompleta (
  input  a,
  input  b,
  input  vemum,
  output s,
  output Cout
);

  wire meiadiferenca_1_s, meiadiferenca_1_vemum, meiadiferenca_2_vemum;

  MeiaDiferenca meiadiferenca_1 (.a(a), .b(b), .s(meiadiferenca_1_s), .vemum(meiadiferenca_1_vemum));
  MeiaDiferenca meiadiferenca_2 (.a(meiadiferenca_1_s), .b(vemum), .s(s), .vemum(meiadiferenca_2_vemum));
  or or_1 (Cout, meiadiferenca_2_vemum, meiadiferenca_1_vemum);

  // Notes on the sheet:
  //   Bruno César Lopes Silva - 415985
endmodule

module Diferenca (
  input  [3:0] b,
  input  [3:0] a,
  output Overflow,
  output COut,
  output [3:0] s
);

  wire diferencacompleta_2_cout, diferencacompleta_3_cout, meiadiferenca_1_vemum;

  xor xor_1 (Overflow, COut, diferencacompleta_2_cout);
  DiferencaCompleta diferencacompleta_1 (.a(a[3]), .b(b[3]), .vemum(diferencacompleta_2_cout), .s(s[3]), .Cout(COut));
  DiferencaCompleta diferencacompleta_2 (
    .a(a[2]), .b(b[2]), .vemum(diferencacompleta_3_cout), .s(s[2]), .Cout(diferencacompleta_2_cout));
  DiferencaCompleta diferencacompleta_3 (
    .a(a[1]), .b(b[1]), .vemum(meiadiferenca_1_vemum), .s(s[1]), .Cout(diferencacompleta_3_cout));
  MeiaDiferenca meiadiferenca_1 (.a(a[0]), .b(b[0]), .s(s[0]), .vemum(meiadiferenca_1_vemum));

  // Notes on the sheet:
  //   Bruno César Lopes Silva - 415985
endmodule

module ComparadorAritmetico (
  input  [3:0] b,
  input  [3:0] a,
  output a_b,
  output a_b_2,
  output a_b_3
);

  wire [2:0] diferenca_1_s;

  Comparador comparador_1 (.b(b), .a(a), .s(a_b_3));
  Diferenca diferenca_1 (.b(b), .a(a), .s({a_b, diferenca_1_s}));  // open: Overflow, COut
  nor nor_1 (a_b_2, a_b, a_b_3);

  // Notes on the sheet:
  //   Bruno César Lopes Silva - 415985
endmodule

module ALU2 (
  input  [3:0] b,
  input  [3:0] a,
  output a_b,
  output a_b_2,
  output a_b_3,
  output OVF,
  output COut,
  output [3:0] s
);

  Diferenca diferenca_1 (.b(b), .a(a), .Overflow(OVF), .COut(COut), .s(s));
  ComparadorAritmetico comparadoraritmetico_1 (.b(b), .a(a), .a_b(a_b), .a_b_2(a_b_2), .a_b_3(a_b_3));

  // Notes on the sheet:
  //   Bruno César Lopes Silva - 415985
endmodule

module Complemento1 (
  input  [3:0] a,
  output [3:0] Comp1
);

  assign Comp1 = ~a;  // NOT_Gate not_1, 4 bits wide

  // Notes on the sheet:
  //   Bruno César Lopes Silva - 415985
endmodule

module Complemento2 (
  input  [3:0] a,
  output Carry,
  output [3:0] Comp2
);

  wire meiasoma_2_cout, meiasoma_3_cout, meiasoma_4_cout, not_1_out, not_2_out, not_3_out, not_4_out;

  MeiaSoma meiasoma_1 (.a(not_1_out), .b(meiasoma_2_cout), .s(Comp2[3]), .COut(Carry));
  not not_1 (not_1_out, a[3]);
  MeiaSoma meiasoma_2 (.a(not_2_out), .b(meiasoma_3_cout), .s(Comp2[2]), .COut(meiasoma_2_cout));
  not not_2 (not_2_out, a[2]);
  not not_3 (not_3_out, a[1]);
  MeiaSoma meiasoma_3 (.a(not_3_out), .b(meiasoma_4_cout), .s(Comp2[1]), .COut(meiasoma_3_cout));
  not not_4 (not_4_out, a[0]);
  MeiaSoma meiasoma_4 (.a(not_4_out), .b(1'b1), .s(Comp2[0]), .COut(meiasoma_4_cout));

  // Notes on the sheet:
  //   Bruno César Lopes Silva - 415985
endmodule

module Incremento (
  input  [3:0] a,
  output Carry,
  output [3:0] Increm
);

  wire meiasoma_2_cout, meiasoma_3_cout, meiasoma_4_cout;

  MeiaSoma meiasoma_1 (.a(a[3]), .b(meiasoma_2_cout), .s(Increm[3]), .COut(Carry));
  MeiaSoma meiasoma_2 (.a(a[2]), .b(meiasoma_3_cout), .s(Increm[2]), .COut(meiasoma_2_cout));
  MeiaSoma meiasoma_3 (.a(a[1]), .b(meiasoma_4_cout), .s(Increm[1]), .COut(meiasoma_3_cout));
  MeiaSoma meiasoma_4 (.a(a[0]), .b(1'b1), .s(Increm[0]), .COut(meiasoma_4_cout));

  // Notes on the sheet:
  //   Bruno César Lopes Silva - 415985
endmodule

module Decremento (
  input  [3:0] a,
  output Carry,
  output [3:0] Decrem
);

  wire meiadiferenca_2_vemum, meiadiferenca_3_vemum, meiadiferenca_4_vemum;

  MeiaDiferenca meiadiferenca_1 (.a(a[3]), .b(meiadiferenca_2_vemum), .s(Decrem[3]), .vemum(Carry));
  MeiaDiferenca meiadiferenca_2 (.a(a[2]), .b(meiadiferenca_3_vemum), .s(Decrem[2]), .vemum(meiadiferenca_2_vemum));
  MeiaDiferenca meiadiferenca_3 (.a(a[1]), .b(meiadiferenca_4_vemum), .s(Decrem[1]), .vemum(meiadiferenca_3_vemum));
  MeiaDiferenca meiadiferenca_4 (.a(a[0]), .b(1'b1), .s(Decrem[0]), .vemum(meiadiferenca_4_vemum));

  // Notes on the sheet:
  //   Bruno César Lopes Silva - 415985
endmodule

module ProdutoPor2 (
  input  [3:0] a,
  output [4:0] Produto_por_2
);

  and and_1 (Produto_por_2[4], a[3], 1'b1);
  and and_2 (Produto_por_2[3], a[2], 1'b1);
  and and_3 (Produto_por_2[2], a[1], 1'b1);
  and and_4 (Produto_por_2[1], a[0], 1'b1);

  assign Produto_por_2[0] = 1'b0;

  // Notes on the sheet:
  //   Bruno César Lopes Silva - 415985
endmodule

module ALUFinal (
  input  [3:0] b,
  input  [3:0] a,
  output a_b,
  output a_b_2,
  output a_b_3,
  output Comparar,
  output OVF,
  output COut,
  output [3:0] s_soma,
  output OVF_2,
  output COut_2,
  output [3:0] s_diferenca,
  output [3:0] Complemento_1,
  output C,
  output [3:0] Compl2,
  output C_2,
  output [3:0] Increm,
  output C_3,
  output [3:0] Decrem,
  output [4:0] Produto_por_2
);

  ALU alu_1 (.b(b), .a(a), .comparador(Comparar), .OVF(OVF), .COut(COut), .s(s_soma));
  ALU2 alu2_1 (.b(b), .a(a), .OVF(OVF_2), .COut(COut_2), .s(s_diferenca), .a_b(a_b), .a_b_2(a_b_2), .a_b_3(a_b_3));
  Complemento1 complemento1_1 (.a(a), .Comp1(Complemento_1));
  ProdutoPor2 produtopor2_1 (.a(a), .Produto_por_2(Produto_por_2));
  Complemento2 complemento2_1 (.a(a), .Carry(C), .Comp2(Compl2));
  Incremento incremento_1 (.a(a), .Carry(C_2), .Increm(Increm));
  Decremento decremento_1 (.a(a), .Carry(C_3), .Decrem(Decrem));

  // Notes on the sheet:
  //   1 - Iguais
  //   0 - Diferentes
  //   Bruno César Lopes Silva - 415985
  //   soma
  //   diferenca
endmodule
