// Logisim project Guia 7.circ as structural Verilog: 5 circuits, main circuit Guia 7
module Guia_7 (
  input  a4,
  input  a3,
  input  a2,
  input  a1,
  input  a0,
  input  in_6,
  input  in_7,
  output s0,
  output s1,
  output s2,
  output s3,
  output s4,
  output w0,
  output w1,
  output w2,
  output w3,
  output w4,
  output w5,
  output z0,
  output z1,
  output z2,
  output z3,
  output z4,
  output z5
);

  Complemento_1 complemento_1_1 (
    .a0(a0), .a1(a1), .a2(a2), .a3(a3), .a4(a4), .s0(s0), .s1(s1), .s2(s2), .s3(s3), .s4(s4));
  Complemento_2 complemento_2_1 (
    .Always_1(in_6), .a0(a0), .a1(a1), .a2(a2), .a3(a3), .a4(a4), .s0(w0), .s1(w1), .s2(w2), .s3(w3),
    .s4(w4), .s5(w5));
  Incremento_1 incremento_1_1 (
    .Always_1(in_7), .a0(a0), .a1(a1), .a2(a2), .a3(a3), .a4(a4), .s0(z0), .s1(z1), .s2(z2), .s3(z3),
    .s4(z4), .s5(z5));

  // Notes on the sheet:
  //   Nome: Bruno Rafael Nicolletti
endmodule

module Complemento_1 (
  input  a0,
  input  a1,
  input  a2,
  input  a3,
  input  a4,
  output s0,
  output s1,
  output s2,
  output s3,
  output s4
);

  not not_1 (s0, a0);
  not not_2 (s1, a1);
  not not_3 (s2, a2);
  not not_4 (s3, a3);
  not not_5 (s4, a4);

  // Notes on the sheet:
  //   Nome: Bruno Rafael Nicolletti
endmodule

module subcircuitoMeia (
  input  a,
  input  b,
  output s0,
  output s1
);

  xor xor_1 (s0, a, b);
  and and_1 (s1, a, b);

  // Notes on the sheet:
  //   Nome: Bruno Rafael Nicolletti
endmodule

module Complemento_2 (
  input  Always_1,
  input  a0,
  input  a1,
  input  a2,
  input  a3,
  input  a4,
  output s0,
  output s1,
  output s2,
  output s3,
  output s4,
  output s5
);

  wire not_1_out, not_2_out, not_3_out, not_4_out, not_5_out, subcircuitomeia_1_s1, subcircuitomeia_2_s1,
       subcircuitomeia_3_s1, subcircuitomeia_4_s1;

  not not_1 (not_1_out, a0);
  not not_2 (not_2_out, a1);
  not not_3 (not_3_out, a2);
  not not_4 (not_4_out, a3);
  not not_5 (not_5_out, a4);
  subcircuitoMeia subcircuitomeia_1 (.a(Always_1), .b(not_1_out), .s0(s0), .s1(subcircuitomeia_1_s1));
  subcircuitoMeia subcircuitomeia_2 (.a(subcircuitomeia_1_s1), .b(not_2_out), .s0(s1), .s1(subcircuitomeia_2_s1));
  subcircuitoMeia subcircuitomeia_3 (.a(subcircuitomeia_2_s1), .b(not_3_out), .s0(s2), .s1(subcircuitomeia_3_s1));
  subcircuitoMeia subcircuitomeia_4 (.a(subcircuitomeia_3_s1), .b(not_4_out), .s0(s3), .s1(subcircuitomeia_4_s1));
  subcircuitoMeia subcircuitomeia_5 (.a(subcircuitomeia_4_s1), .b(not_5_out), .s0(s4), .s1(s5));

  // Notes on the sheet:
  //   Nome: Bruno Rafael Nicolletti
endmodule

module Incremento_1 (
  input  Always_1,
  input  a0,
  input  a1,
  input  a2,
  input  a3,
  input  a4,
  output s0,
  output s1,
  output s2,
  output s3,
  output s4,
  output s5
);

  wire subcircuitomeia_1_s1, subcircuitomeia_2_s1, subcircuitomeia_3_s1, subcircuitomeia_4_s1;

  subcircuitoMeia subcircuitomeia_1 (.a(Always_1), .b(a0), .s0(s0), .s1(subcircuitomeia_1_s1));
  subcircuitoMeia subcircuitomeia_2 (.a(subcircuitomeia_1_s1), .b(a1), .s0(s1), .s1(subcircuitomeia_2_s1));
  subcircuitoMeia subcircuitomeia_3 (.a(subcircuitomeia_2_s1), .b(a2), .s0(s2), .s1(subcircuitomeia_3_s1));
  subcircuitoMeia subcircuitomeia_4 (.a(subcircuitomeia_3_s1), .b(a3), .s0(s3), .s1(subcircuitomeia_4_s1));
  subcircuitoMeia subcircuitomeia_5 (.a(subcircuitomeia_4_s1), .b(a4), .s0(s4), .s1(s5));

  // Notes on the sheet:
  //   Nome: Bruno Rafael Nicolletti
endmodule
