// Logisim project Guia07.circ as structural Verilog: 5 circuits, main circuit ALU
module ALU (
  input  [4:0] A,
  input  [4:0] B,
  input  Sub,
  output [5:0] S,
  output Diferente,
  output Igual,
  output A___B,
  output A___B_2,
  output Carry,
  output Overflow,
  output Zero,
  output [4:0] complemento1,
  output [5:0] complemento2,
  output [5:0] Incremento1
);

  wire full_adder_1_s1, full_adder_2_s1, full_adder_3_s1, full_adder_4_s1, not_2_out, xor_1_out, xor_2_out,
       xor_3_out, xor_4_out, xor_5_out;

  incremento1 incremento1_1 (.in_1(complemento1), .out_2(complemento2));
  assign complemento1 = ~B;  // NOT_Gate not_1, 5 bits wide
  incremento1 incremento1_2 (.in_1(B), .out_2(Incremento1));
  xor xor_1 (xor_1_out, B[4], Sub);
  xor xor_2 (xor_2_out, B[3], Sub);
  xor xor_3 (xor_3_out, B[2], Sub);
  xor xor_4 (xor_4_out, B[1], Sub);
  xor xor_5 (xor_5_out, B[0], Sub);
  comparador comparador_1 (
    .a0(A[4]), .b0(B[4]), .a1(A[3]), .b1(B[3]), .a2(A[2]), .b2(B[2]), .a3(A[1]), .b3(B[1]), .a4(A[0]),
    .b4(B[0]), .A_B(A___B_2), .A_B_2(A___B), .Igual(Igual), .Diferente(Diferente));
  full_adder full_adder_1 (.A(A[4]), .B(xor_1_out), .Cin(Sub), .s0(S[0]), .s1(full_adder_1_s1));
  full_adder full_adder_2 (.A(A[3]), .B(xor_2_out), .Cin(full_adder_1_s1), .s0(S[1]), .s1(full_adder_2_s1));
  full_adder full_adder_3 (.A(A[2]), .B(xor_3_out), .Cin(full_adder_2_s1), .s0(S[2]), .s1(full_adder_3_s1));
  full_adder full_adder_4 (.A(A[1]), .B(xor_4_out), .Cin(full_adder_3_s1), .s0(S[3]), .s1(full_adder_4_s1));
  full_adder full_adder_5 (.A(A[0]), .B(xor_5_out), .Cin(full_adder_4_s1), .s0(S[4]), .s1(Carry));
  not not_2 (not_2_out, full_adder_4_s1);
  and and_1 (Overflow, Carry, not_2_out);
  nor nor_1 (Zero, S[0], S[1], S[2], S[3], S[4], S[5]);
  xor xor_6 (S[5], Carry, Sub);

  // Notes on the sheet:
  //   Caio Ragacci Pimentel - 405794
  //   Guia07
endmodule

module half_adder (
  input  A,
  input  B,
  output s0,
  output s1
);

  wire not_1_out, or_1_out;

  or or_1 (or_1_out, A, B);
  and and_1 (s1, A, B);
  not not_1 (not_1_out, s1);
  and and_2 (s0, or_1_out, or_1_out, not_1_out);

  // Notes on the sheet:
  //   Caio Ragacci Pimentel - 405794
  //   Guia07
endmodule

module full_adder (
  input  A,
  input  B,
  input  Cin,
  output s0,
  output s1
);

  wire half_adder_1_s0, half_adder_1_s1, half_adder_2_s1;

  half_adder half_adder_1 (.A(A), .B(B), .s0(half_adder_1_s0), .s1(half_adder_1_s1));
  half_adder half_adder_2 (.A(half_adder_1_s0), .B(Cin), .s0(s0), .s1(half_adder_2_s1));
  or or_1 (s1, half_adder_2_s1, half_adder_1_s1);

  // Notes on the sheet:
  //   Caio Ragacci Pimentel - 405794
  //   Guia07
endmodule

module comparador (
  input  a0,
  input  b0,
  input  a1,
  input  b1,
  input  a2,
  input  b2,
  input  a3,
  input  b3,
  input  a4,
  input  b4,
  output A_B,
  output A_B_2,
  output Igual,
  output Diferente
);

  wire and_1_out, and_2_out, and_3_out, and_4_out, and_5_out, and_6_out, and_7_out, and_8_out, and_9_out,
       and_10_out, and_11_out, and_12_out, and_13_out, and_14_out, and_15_out, and_16_out, and_17_out,
       and_18_out, nor_1_out, nor_2_out, nor_3_out, nor_4_out, nor_5_out, not_1_out, not_2_out, not_3_out,
       not_4_out, not_5_out, not_6_out, not_7_out, not_8_out, not_9_out, not_10_out;

  not not_1 (not_1_out, a0);
  not not_2 (not_2_out, b0);
  not not_3 (not_3_out, a1);
  not not_4 (not_4_out, b1);
  not not_5 (not_5_out, a2);
  not not_6 (not_6_out, b2);
  not not_7 (not_7_out, a3);
  not not_8 (not_8_out, b3);
  not not_9 (not_9_out, a4);
  not not_10 (not_10_out, b4);
  and and_1 (and_1_out, not_1_out, b0);
  and and_2 (and_2_out, a0, not_2_out);
  and and_3 (and_3_out, not_3_out, b1);
  and and_4 (and_4_out, a1, not_4_out);
  and and_5 (and_5_out, not_5_out, b2);
  and and_6 (and_6_out, a2, not_6_out);
  and and_7 (and_7_out, not_7_out, b3);
  and and_8 (and_8_out, a3, not_8_out);
  and and_9 (and_9_out, not_9_out, b4);
  and and_10 (and_10_out, a4, not_10_out);
  nor nor_1 (nor_1_out, and_1_out, and_2_out);
  nor nor_2 (nor_2_out, and_3_out, and_4_out);
  nor nor_3 (nor_3_out, and_5_out, and_6_out);
  nor nor_4 (nor_4_out, and_7_out, and_8_out);
  nor nor_5 (nor_5_out, and_9_out, and_10_out);
  and and_11 (and_11_out, and_3_out, nor_1_out);
  and and_12 (and_12_out, and_4_out, nor_1_out);
  and and_13 (and_13_out, and_5_out, nor_1_out, nor_2_out);
  and and_14 (and_14_out, and_6_out, nor_1_out, nor_2_out);
  and and_15 (and_15_out, and_7_out, nor_1_out, nor_2_out, nor_3_out);
  and and_16 (and_16_out, nor_1_out, nor_2_out, and_8_out, nor_3_out);
  and and_17 (and_17_out, and_9_out, nor_1_out, nor_2_out, nor_3_out, nor_4_out);
  and and_18 (and_18_out, nor_1_out, nor_2_out, and_10_out, nor_2_out, nor_4_out);
  and and_19 (Igual, nor_1_out, nor_2_out, nor_3_out, nor_4_out, nor_5_out);
  or or_1 (A_B, and_1_out, and_15_out, and_13_out, and_17_out);
  or or_2 (A_B_2, and_2_out, and_14_out, and_16_out, and_18_out);
  not not_11 (Diferente, Igual);

  // Notes on the sheet:
  //   Caio Ragacci Pimentel - 405794
  //   Guia07
endmodule

module incremento1 (
  input  [4:0] in_1,
  output [5:0] out_2
);

  wire half_adder_1_s1, half_adder_2_s1, half_adder_3_s1, half_adder_4_s1;

  half_adder half_adder_1 (.A(in_1[0]), .B(1'b1), .s0(out_2[0]), .s1(half_adder_1_s1));
  half_adder half_adder_2 (.A(in_1[1]), .B(half_adder_1_s1), .s0(out_2[1]), .s1(half_adder_2_s1));
  half_adder half_adder_3 (.A(in_1[2]), .B(half_adder_2_s1), .s0(out_2[2]), .s1(half_adder_3_s1));
  half_adder half_adder_4 (.A(in_1[3]), .B(half_adder_3_s1), .s0(out_2[3]), .s1(half_adder_4_s1));
  half_adder half_adder_5 (.A(in_1[4]), .B(half_adder_4_s1), .s0(out_2[4]), .s1(out_2[5]));

  // Notes on the sheet:
  //   Caio Ragacci Pimentel - 405794
  //   Guia07
endmodule
