// Logisim project alu.circ as structural Verilog
// HA
module half_adder (
  input  A,
  input  B,
  output S,
  output Cout
);

  and and_1 (Cout, A, B);
  xor xor_1 (S, A, B);
endmodule

// FA
module full_adder (
  input  A,
  input  B,
  input  Cin,
  output S,
  output Cout
);

  wire and_1_out, and_2_out, xor_1_out;

  xor xor_1 (xor_1_out, B, Cin);
  xor xor_2 (S, A, xor_1_out);
  and and_1 (and_1_out, xor_1_out, A);
  and and_2 (and_2_out, B, Cin);
  or or_1 (Cout, and_1_out, and_2_out);
endmodule

// HS
module half_subtractor (
  input  A,
  input  B,
  output S,
  output Bout
);

  wire not_1_out;

  not not_1 (not_1_out, A);
  xor xor_1 (S, A, B);
  and and_1 (Bout, not_1_out, B);
endmodule

// FS
module full_subtractor (
  input  A,
  input  B,
  input  Bin,
  output S,
  output Bout
);

  wire and_1_out, and_2_out, not_1_out, xor_1_out;

  xor xor_1 (xor_1_out, B, Bin);
  xor xor_2 (S, A, xor_1_out);
  and and_1 (and_1_out, xor_1_out, not_1_out);
  not not_1 (not_1_out, A);
  and and_2 (and_2_out, B, Bin);
  or or_1 (Bout, and_1_out, and_2_out);
endmodule

// +
module _5bit_adder (
  input  [4:0] A,
  input  [4:0] B,
  output [4:0] S,
  output Cout
);

  wire full_adder_1_cout, full_adder_2_cout, full_adder_3_cout, half_adder_1_cout;

  half_adder half_adder_1 (.A(A[0]), .B(B[0]), .S(S[0]), .Cout(half_adder_1_cout));
  full_adder full_adder_1 (.A(half_adder_1_cout), .B(A[1]), .Cin(B[1]), .S(S[1]), .Cout(full_adder_1_cout));
  full_adder full_adder_2 (.A(full_adder_1_cout), .B(A[2]), .Cin(B[2]), .S(S[2]), .Cout(full_adder_2_cout));
  full_adder full_adder_3 (.A(full_adder_2_cout), .B(A[3]), .Cin(B[3]), .S(S[3]), .Cout(full_adder_3_cout));
  full_adder full_adder_4 (.A(full_adder_3_cout), .B(A[4]), .Cin(B[4]), .S(S[4]), .Cout(Cout));
endmodule

// -
module _5bit_subtractor (
  input  [4:0] A,
  input  [4:0] B,
  output [4:0] S,
  output Bout
);

  wire full_subtractor_1_bout, full_subtractor_2_bout, full_subtractor_3_bout, half_subtractor_1_bout;

  half_subtractor half_subtractor_1 (.A(A[0]), .B(B[0]), .S(S[0]), .Bout(half_subtractor_1_bout));
  full_subtractor full_subtractor_1 (
    .A(A[1]), .B(B[1]), .Bin(half_subtractor_1_bout), .S(S[1]), .Bout(full_subtractor_1_bout));
  full_subtractor full_subtractor_2 (
    .A(A[2]), .B(B[2]), .Bin(full_subtractor_1_bout), .S(S[2]), .Bout(full_subtractor_2_bout));
  full_subtractor full_subtractor_3 (
    .A(A[3]), .B(B[3]), .Bin(full_subtractor_2_bout), .S(S[3]), .Bout(full_subtractor_3_bout));
  full_subtractor full_subtractor_4 (.A(A[4]), .B(B[4]), .Bin(full_subtractor_3_bout), .S(S[4]), .Bout(Bout));
endmodule

// LC
module _5bit_logic_comparator (
  input  [4:0] A,
  input  [4:0] B,
  output S
);

  wire xnor_1_out, xnor_2_out, xnor_3_out, xnor_4_out, xnor_5_out;

  xnor xnor_1 (xnor_1_out, A[0], B[0]);
  xnor xnor_2 (xnor_2_out, A[1], B[1]);
  xnor xnor_3 (xnor_3_out, A[2], B[2]);
  xnor xnor_4 (xnor_4_out, A[3], B[3]);
  xnor xnor_5 (xnor_5_out, A[4], B[4]);
  and and_1 (S, xnor_1_out, xnor_2_out, xnor_3_out, xnor_4_out, xnor_5_out);
endmodule

// AC
module _5bit_arithmetic_comparator (
  input  [4:0] A___B,
  output A___B_2,
  output A___B_3,
  output A___B_4
);

  wire bitselector_1_out, not_1_out, not_2_out;

  BitSelector #(.width(5)) bitselector_1 (.in(A___B), .out(bitselector_1_out), .sel(3'b100));
  nor nor_1 (A___B_4, A___B[0], A___B[1], A___B[2], A___B[3], A___B[4]);
  not not_1 (not_1_out, bitselector_1_out);
  and and_1 (A___B_2, not_1_out, not_2_out);
  and and_2 (A___B_3, bitselector_1_out, not_2_out);
  not not_2 (not_2_out, A___B_4);
endmodule

// 2's
module _5bit_2_s_complement (
  input  [4:0] A,
  output [4:0] out_2
);

  wire [4:0] not_1_out;

  assign not_1_out = ~A;  // NOT_Gate not_1, 5 bits wide
  _5bit_adder u_5bit_adder_1 (.A(not_1_out), .B(5'b00001), .S(out_2));  // open: Cout
endmodule

// +1
module _5bit_increment (
  input  [4:0] A,
  output [4:0] S,
  output Cout
);

  _5bit_adder u_5bit_adder_1 (.A(A), .B(5'b00001), .S(S), .Cout(Cout));
endmodule

// -1
module _5bit_decrement (
  input  [4:0] A,
  output [4:0] S,
  output Bout
);

  _5bit_subtractor u_5bit_subtractor_1 (.A(A), .B(5'b00001), .S(S), .Bout(Bout));
endmodule

module _5bit_ALU (
  input  [4:0] A,
  input  [4:0] B,
  input  [2:0] Op_code,
  output [4:0] S,
  output Logic_A___B,
  output A___B,
  output A___B_2,
  output A___B_3,
  output Zero,
  output Carry,
  output Overflow
);

  wire and_2_out, and_3_out, bitselector_1_out, bitselector_2_out, multiplexer_3_out, n5bit_adder_1_cout,
       n5bit_decrement_1_bout, n5bit_increment_1_cout, n5bit_subtractor_1_bout, nor_1_out, not_2_out,
       xnor_1_out, xor_1_out;
  wire [4:0] and_1_out, n5bit_2_s_complement_1_out_2, n5bit_adder_1_s, n5bit_decrement_1_s,
       n5bit_increment_1_s, n5bit_subtractor_1_s, not_1_out, or_1_out;

  _5bit_adder u_5bit_adder_1 (.A(A), .B(B), .S(n5bit_adder_1_s), .Cout(n5bit_adder_1_cout));
  _5bit_subtractor u_5bit_subtractor_1 (.A(A), .B(B), .S(n5bit_subtractor_1_s), .Bout(n5bit_subtractor_1_bout));
  assign not_1_out = ~A;  // NOT_Gate not_1, 5 bits wide
  assign and_1_out = A & B;  // AND_Gate and_1, 5 bits wide
  assign or_1_out = A | B;  // OR_Gate or_1, 5 bits wide
  _5bit_2_s_complement u_5bit_2_s_complement_1 (.A(A), .out_2(n5bit_2_s_complement_1_out_2));
  _5bit_increment u_5bit_increment_1 (.A(A), .S(n5bit_increment_1_s), .Cout(n5bit_increment_1_cout));
  _5bit_decrement u_5bit_decrement_1 (.A(A), .S(n5bit_decrement_1_s), .Bout(n5bit_decrement_1_bout));
  _5bit_logic_comparator u_5bit_logic_comparator_1 (.A(A), .B(B), .S(Logic_A___B));
  _5bit_arithmetic_comparator u_5bit_arithmetic_comparator_1 (
    .A___B(n5bit_subtractor_1_s), .A___B_2(A___B), .A___B_3(A___B_2), .A___B_4(A___B_3));
  BitSelector #(.width(5)) bitselector_1 (.in(A), .out(bitselector_1_out), .sel(3'b100));
  BitSelector #(.width(5)) bitselector_2 (.in(B), .out(bitselector_2_out), .sel(3'b100));
  Multiplexer #(.select(3), .width(5), .disabled(0), .enable("false")) multiplexer_1 (
    .in0(n5bit_adder_1_s), .in1(n5bit_subtractor_1_s), .in2(not_1_out), .in3(and_1_out), .in4(or_1_out),
    .in5(n5bit_2_s_complement_1_out_2), .in6(n5bit_increment_1_s), .in7(n5bit_decrement_1_s), .out(S),
    .sel(Op_code));
  not not_2 (not_2_out, S[4]);
  nor nor_1 (nor_1_out, S[0], S[1], S[2], S[3], not_2_out);
  nor nor_2 (Zero, S[0], S[1], S[2], S[3], S[4]);
  xnor xnor_1 (xnor_1_out, bitselector_2_out, bitselector_1_out);
  and and_2 (and_2_out, xnor_1_out, xor_1_out);
  xor xor_1 (xor_1_out, bitselector_1_out, S[4]);
  and and_3 (and_3_out, xor_1_out, xnor_1_out);
  Multiplexer #(.select(3), .disabled(0), .enable("false")) multiplexer_2 (
    .in0(n5bit_adder_1_cout), .in1(n5bit_subtractor_1_bout), .in2(1'b0), .in3(1'b0), .in4(1'b0), .in5(1'b0),
    .in6(n5bit_increment_1_cout), .in7(n5bit_decrement_1_bout), .out(Carry), .sel(Op_code));
  Multiplexer #(.select(3), .disabled(0), .enable("false")) multiplexer_3 (
    .in0(and_2_out), .in1(and_3_out), .in2(1'b0), .in3(1'b0), .in4(1'b0), .in5(1'b0), .in6(1'b0), .in7(1'b0),
    .out(multiplexer_3_out), .sel(Op_code));
  or or_2 (Overflow, multiplexer_3_out, nor_1_out);
endmodule
