// Logisim project incremento e decremento exercicios 3 e 4.circ as structural Verilog: 4 circuits, main circuit main
module main (
  input  x,
  input  y,
  output Vout,
  output s
);

  and and_1 (Vout, y, x);
  xor xor_1 (s, x, y);
endmodule

module Ha (
  input  x,
  input  y,
  input  Vin,
  output Vout,
  output s
);

  wire main_1_s, main_1_vout, main_2_vout;

  or or_1 (Vout, main_1_vout, main_2_vout);
  main main_1 (.Vout(main_1_vout), .x(x), .y(y), .s(main_1_s));
  main main_2 (.Vout(main_2_vout), .x(Vin), .y(main_1_s), .s(s));
endmodule

module Fa (
  input  a3,
  input  b3,
  input  a2,
  input  b2,
  input  a1,
  input  b1,
  input  a0,
  input  b0,
  input  Vin,
  output Vout,
  output s3,
  output s2,
  output s1,
  output s0
);

  wire ha_1_vout, ha_3_vout, ha_4_vout;

  Ha ha_1 (.Vout(ha_1_vout), .x(a2), .y(b2), .s(s2), .Vin(ha_3_vout));
  Ha ha_2 (.Vout(Vout), .x(a3), .y(b3), .s(s3), .Vin(ha_1_vout));
  Ha ha_3 (.Vout(ha_3_vout), .x(a1), .y(b1), .s(s1), .Vin(ha_4_vout));
  Ha ha_4 (.Vout(ha_4_vout), .x(a0), .y(b0), .s(s0), .Vin(Vin));
endmodule

module FA4B (
  input  [3:0] a,
  input  [3:0] b,
  input  Sel1,
  input  Sel2,
  output _1____a___b,
  output _1____a___b_2,
  output _1____a___b_3,
  output detector,
  output Cout,
  output s3,
  output s2,
  output s1,
  output s0,
  output Cout_2,
  output s3_2,
  output s2_2,
  output s1_2,
  output s0_2,
  output Cout_3,
  output s3_3,
  output s2_3,
  output s1_3,
  output s0_3
);

  wire and_3_out, and_4_out, and_5_out, and_6_out, and_7_out, and_8_out, and_9_out, and_10_out, not_1_out,
       not_7_out, not_8_out, not_9_out, not_10_out, not_11_out, not_12_out, not_13_out, not_14_out, or_1_out,
       or_2_out, or_3_out, xnor_1_out, xnor_2_out, xnor_3_out, xnor_4_out, xor_1_out, xor_2_out, xor_3_out,
       xor_4_out;

  xor xor_1 (xor_1_out, Sel1, b[3]);
  not not_1 (not_1_out, Cout_2);
  and and_1 (detector, Sel1, not_1_out);
  not not_2 (s3, s3_2);
  not not_3 (Cout, Cout_2);
  xor xor_2 (xor_2_out, Sel1, b[2]);
  Fa fa_1 (
    .Vout(Cout_2), .a3(a[3]), .b3(xor_1_out), .a2(a[2]), .b2(xor_2_out), .a1(a[1]), .b1(xor_3_out),
    .a0(a[0]), .b0(xor_4_out), .s3(s3_2), .s2(s2_2), .s1(s1_2), .s0(s0_2), .Vin(Sel2));
  not not_4 (s1, s1_2);
  not not_5 (s2, s2_2);
  not not_6 (s0, s0_2);
  xor xor_3 (xor_3_out, Sel1, b[1]);
  xor xor_4 (xor_4_out, Sel1, b[0]);
  xnor xnor_1 (xnor_1_out, b[3], a[3]);
  or or_1 (or_1_out, s3_2, s0_2, s1_2, s2_2);
  xor xor_5 (Cout_3, Cout_2, or_1_out);
  xnor xnor_2 (xnor_2_out, b[2], a[2]);
  or or_2 (or_2_out, s0_2, s1_2, s2_2);
  xor xor_6 (s3_3, s3_2, or_2_out);
  xnor xnor_3 (xnor_3_out, b[1], a[1]);
  and and_2 (_1____a___b, xnor_1_out, xnor_2_out, xnor_3_out, xnor_4_out);
  or or_3 (or_3_out, s1_2, s0_2);
  xor xor_7 (s2_3, s2_2, or_3_out);
  xnor xnor_4 (xnor_4_out, b[0], a[0]);
  xor xor_8 (s1_3, s1_2, s0_2);
  not not_7 (not_7_out, a[3]);
  and and_3 (and_3_out, b[3], not_7_out);
  not not_8 (not_8_out, a[2]);
  and and_4 (and_4_out, b[2], xnor_1_out, not_8_out);
  or or_4 (_1____a___b_2, and_3_out, and_4_out, and_5_out, and_6_out);
  not not_9 (not_9_out, a[1]);
  and and_5 (and_5_out, b[1], xnor_1_out, not_9_out);
  not not_10 (not_10_out, a[0]);
  and and_6 (and_6_out, b[0], xnor_1_out, xnor_2_out, xnor_3_out, not_10_out);
  not not_11 (not_11_out, b[3]);
  and and_7 (and_7_out, not_11_out, a[3]);
  not not_12 (not_12_out, b[2]);
  and and_8 (and_8_out, not_12_out, xnor_1_out, a[2]);
  not not_13 (not_13_out, b[1]);
  and and_9 (and_9_out, not_13_out, xnor_1_out, xnor_2_out, a[1]);
  or or_5 (_1____a___b_3, and_7_out, and_8_out, and_9_out, and_10_out);
  not not_14 (not_14_out, b[0]);
  and and_10 (and_10_out, not_14_out, xnor_3_out, xnor_2_out, xnor_1_out, a[0]);

  assign s0_3 = s0_2;

  // Notes on the sheet:
  //   sel1 = 0 e sel 2 = 0 = > subtracao
  //   sel1 = 1 e sel 2 = 1 = > soma
  //   sel1 = 0 e sel 2 = 1 = > a + b + 1
  //   sel1 = 1 e sel 2 = 0 = > a - b - 1
  //   calcula o complemento de 1
  //   calcula o complemento de 2
  //   0 => a != b
  //   comparador logico
  //   resposta sem complemento
  //   comparadores aritmeticos
endmodule
