// Logisim project Guia07.circ as structural Verilog: 16 circuits, main circuit Half Adder
module MAIN (
  input  [4:0] a,
  input  [4:0] b,
  input  [3:0] Select,
  output [4:0] Resultado,
  output Sinal,
  output Overflow,
  output a___b,
  output b___a,
  output a___b_2,
  output Zero,
  output Carry
);

  ALU_5_Bits alu_5_bits_1 (
    .Resultado(Resultado), .Sinal(Sinal), .Overflow(Overflow), .a___b(a___b), .b___a(b___a),
    .a___b_2(a___b_2), .Zero(Zero), .Carry(Carry), .b(b), .a(a), .Select(Select));  // open: a____b

  // Notes on the sheet:
  //   0000 = a & b
  //   0001 = a | b
  //   0010 = C1(a)
  //   0011 = C1(b)
  //   0100 = C2(a)
  //   0101 = C2(b)
  //   0110 = a + 1
  //   0111 = b + 1
  //   1000 = a - 1
  //   1001 = b - 1
  //   1010 = 2 * a
  //   1011 = 2 * b
  //   1100 = a + b
  //   1101 = a - b
  //   1110 = a + b
  //   1111 = a - b
  //   Erro para calcular Overflow em alguns casos
endmodule

module Half_Adder (
  input  a,
  input  b,
  output Soma,
  output Cout
);

  xor xor_1 (Soma, a, b);
  and and_1 (Cout, a, b);

  // Notes on the sheet:
  //   Douglas de Loredo Borges - 417889
endmodule

module Full_Adder (
  input  a,
  input  b,
  input  Cin,
  output Soma,
  output Cout
);

  wire half_adder_1_cout, half_adder_1_soma, half_adder_2_cout;

  Half_Adder half_adder_1 (.Soma(half_adder_1_soma), .Cout(half_adder_1_cout), .a(a), .b(b));
  Half_Adder half_adder_2 (.Soma(Soma), .Cout(half_adder_2_cout), .a(half_adder_1_soma), .b(Cin));
  or or_1 (Cout, half_adder_2_cout, half_adder_1_cout);

  // Notes on the sheet:
  //   Douglas de Loredo Borges - 417889
endmodule

module Full_Adder_5_Bits (
  input  [4:0] a,
  input  [4:0] b,
  output [5:0] Soma
);

  wire full_adder_1_cout, full_adder_2_cout, full_adder_3_cout, half_adder_1_cout;

  Half_Adder half_adder_1 (.Soma(Soma[0]), .Cout(half_adder_1_cout), .a(a[0]), .b(b[0]));
  Full_Adder full_adder_1 (.Soma(Soma[1]), .Cout(full_adder_1_cout), .a(a[1]), .b(b[1]), .Cin(half_adder_1_cout));
  Full_Adder full_adder_2 (.Soma(Soma[2]), .Cout(full_adder_2_cout), .a(a[2]), .b(b[2]), .Cin(full_adder_1_cout));
  Full_Adder full_adder_3 (.Soma(Soma[3]), .Cout(full_adder_3_cout), .a(a[3]), .b(b[3]), .Cin(full_adder_2_cout));
  Full_Adder full_adder_4 (.Soma(Soma[4]), .Cout(Soma[5]), .a(a[4]), .b(b[4]), .Cin(full_adder_3_cout));

  // Notes on the sheet:
  //   Douglas de Loredo Borges - 417889
endmodule

module Half_Subtractor (
  input  a,
  input  b,
  output \Diferença ,
  output Vout
);

  wire not_1_out;

  xor xor_1 (\Diferença , a, b);
  not not_1 (not_1_out, a);
  and and_1 (Vout, not_1_out, b);

  // Notes on the sheet:
  //   Douglas de Loredo Borges - 417889
endmodule

module Full_Subtractor (
  input  a,
  input  b,
  input  Vin,
  output \Diferença ,
  output Vout
);

  wire \half_subtractor_1_diferença , half_subtractor_1_vout, half_subtractor_2_vout;

  Half_Subtractor half_subtractor_1 (
    .\Diferença (\half_subtractor_1_diferença ), .Vout(half_subtractor_1_vout), .a(a), .b(b));
  Half_Subtractor half_subtractor_2 (
    .\Diferença (\Diferença ), .Vout(half_subtractor_2_vout), .a(\half_subtractor_1_diferença ), .b(Vin));
  or or_1 (Vout, half_subtractor_2_vout, half_subtractor_1_vout);

  // Notes on the sheet:
  //   Douglas de Loredo Borges - 417889
endmodule

module Full_Subtractor_5_Bits (
  input  [4:0] a,
  input  [4:0] b,
  output [5:0] \Diferença 
);

  wire full_subtractor_1_vout, full_subtractor_2_vout, full_subtractor_3_vout, half_subtractor_1_vout;

  Half_Subtractor half_subtractor_1 (.\Diferença (\Diferença [0]), .Vout(half_subtractor_1_vout), .a(a[0]), .b(b[0]));
  Full_Subtractor full_subtractor_1 (
    .\Diferença (\Diferença [1]), .Vout(full_subtractor_1_vout), .a(a[1]), .b(b[1]),
    .Vin(half_subtractor_1_vout));
  Full_Subtractor full_subtractor_2 (
    .\Diferença (\Diferença [2]), .Vout(full_subtractor_2_vout), .a(a[2]), .b(b[2]),
    .Vin(full_subtractor_1_vout));
  Full_Subtractor full_subtractor_3 (
    .\Diferença (\Diferença [3]), .Vout(full_subtractor_3_vout), .a(a[3]), .b(b[3]),
    .Vin(full_subtractor_2_vout));
  Full_Subtractor full_subtractor_4 (
    .\Diferença (\Diferença [4]), .Vout(\Diferença [5]), .a(a[4]), .b(b[4]), .Vin(full_subtractor_3_vout));

  // Notes on the sheet:
  //   Douglas de Loredo Borges - 417889
endmodule

module Signal_Flag_5_Bits (
  input  [3:0] Select,
  input  [4:0] a,
  input  [4:0] b,
  input  Op,
  input  [5:0] a_b___a_b,
  output Sinal
);

  wire and_1_out, and_2_out, and_3_out, and_4_out, and_5_out, and_6_out, and_7_out, and_8_out, and_9_out,
       and_10_out, and_11_out, and_12_out, and_13_out, nor_1_out, not_1_out, not_2_out, not_3_out, not_4_out,
       not_5_out, not_6_out, not_7_out, not_8_out, not_9_out, not_10_out, not_11_out, not_12_out, not_13_out,
       not_14_out, not_15_out, not_16_out, not_17_out, not_18_out, not_19_out, not_20_out, not_21_out,
       not_22_out, not_23_out, not_24_out, not_25_out, not_26_out, not_27_out, not_28_out, not_29_out,
       or_1_out, or_2_out, or_3_out, or_4_out, or_5_out, undriven;

  not not_1 (not_1_out, Select[3]);
  not not_2 (not_2_out, Select[2]);
  not not_3 (not_3_out, Select[1]);
  not not_4 (not_4_out, Select[0]);
  not not_5 (not_5_out, Select[3]);
  not not_6 (not_6_out, Select[2]);
  not not_7 (not_7_out, Select[1]);
  or or_1 (or_1_out, a[4], a[1]);
  not not_8 (not_8_out, Select[3]);
  not not_9 (not_9_out, Select[2]);
  not not_10 (not_10_out, Select[0]);
  not not_11 (not_11_out, a[4]);
  not not_12 (not_12_out, Select[3]);
  not not_13 (not_13_out, Select[2]);
  not not_14 (not_14_out, a[1]);
  not not_15 (not_15_out, Select[3]);
  not not_16 (not_16_out, Select[1]);
  not not_17 (not_17_out, Select[0]);
  not not_18 (not_18_out, a[4]);
  or or_2 (or_2_out, a[4], a[3], a[2], a[1], a[0]);
  not not_19 (not_19_out, Select[3]);
  not not_20 (not_20_out, Select[1]);
  not not_21 (not_21_out, a[1]);
  or or_3 (or_3_out, a[1], a[0], b[2], b[1], b[0]);
  and and_1 (and_1_out, not_1_out, not_2_out, not_3_out, not_4_out, a[4], a[1]);
  and and_2 (and_2_out, not_5_out, not_6_out, not_7_out, Select[0], or_1_out);
  and and_3 (and_3_out, not_8_out, not_9_out, Select[1], not_10_out, not_11_out);
  or or_4 (or_4_out, and_1_out, and_2_out, and_3_out, and_4_out, and_5_out, and_6_out);
  and and_4 (and_4_out, not_12_out, not_13_out, Select[1], Select[0], not_14_out);
  and and_5 (and_5_out, not_15_out, Select[2], not_16_out, not_17_out, or_2_out, not_18_out);
  and and_6 (and_6_out, not_19_out, Select[2], not_20_out, Select[0], or_3_out, not_21_out);
  not not_22 (not_22_out, Op);
  not not_23 (not_23_out, Op);
  not not_24 (not_24_out, a[1]);
  not not_25 (not_25_out, a[1]);
  nor nor_1 (nor_1_out, and_7_out, and_13_out);
  and and_7 (and_7_out, not_26_out, not_27_out);
  not not_26 (not_26_out, Select[1]);
  not not_27 (not_27_out, Select[3]);
  and and_8 (and_8_out, undriven, a_b___a_b[4], nor_1_out);
  and and_9 (and_9_out, undriven, a[1], not_22_out, nor_1_out);
  and and_10 (and_10_out, a[1], not_23_out, a_b___a_b[4], nor_1_out);
  and and_11 (and_11_out, not_24_out, Op, a_b___a_b[4], nor_1_out);
  and and_12 (and_12_out, undriven, not_25_out, Op, nor_1_out);
  and and_13 (and_13_out, not_29_out, not_28_out);
  not not_28 (not_28_out, Select[3]);
  not not_29 (not_29_out, Select[2]);
  or or_5 (or_5_out, and_8_out, and_9_out, and_10_out, and_11_out, and_12_out);
  or or_6 (Sinal, or_5_out, or_4_out);

  assign b[4:3] = a[1:0];

  // Notes on the sheet:
  //   Douglas de Loredo Borges - 417889
endmodule

module Overflow_Flag_5_Bits (
  input  [3:0] Select,
  input  [4:0] a,
  input  [4:0] b,
  input  Op,
  input  [5:0] a_b___a_b,
  output Overflow
);

  wire and_1_out, and_2_out, and_3_out, and_4_out, and_5_out, and_6_out, and_7_out, nor_1_out, not_1_out,
       not_2_out, not_3_out, not_4_out, not_5_out, not_6_out, not_7_out, not_8_out, not_9_out, not_10_out,
       not_11_out, not_12_out, not_13_out, or_1_out, undriven;

  and and_1 (and_1_out, undriven, a[1], not_1_out, not_2_out);
  not not_1 (not_1_out, Op);
  not not_2 (not_2_out, a_b___a_b[4]);
  not not_3 (not_3_out, undriven);
  not not_4 (not_4_out, a[1]);
  and and_2 (and_2_out, not_3_out, not_4_out, not_5_out, a_b___a_b[4]);
  not not_5 (not_5_out, Op);
  not not_6 (not_6_out, undriven);
  and and_3 (and_3_out, not_6_out, a[1], Op, a_b___a_b[4]);
  not not_7 (not_7_out, a[1]);
  and and_4 (and_4_out, undriven, not_7_out, Op, not_8_out);
  not not_8 (not_8_out, a_b___a_b[4]);
  not not_9 (not_9_out, Select[3]);
  and and_5 (and_5_out, not_9_out, not_10_out);
  not not_10 (not_10_out, Select[2]);
  not not_11 (not_11_out, Select[3]);
  and and_6 (and_6_out, not_11_out, not_12_out);
  not not_12 (not_12_out, Select[1]);
  not not_13 (not_13_out, Select[3]);
  and and_7 (and_7_out, not_13_out, Select[2], Select[1], undriven, a[1]);
  // NOT_Gate not_14 is placed but not wired
  // AND_Gate and_8 is placed but not wired
  // NOT_Gate not_15 is placed but not wired
  // NOT_Gate not_16 is placed but not wired
  or or_1 (or_1_out, and_1_out, and_2_out, and_3_out, and_4_out);
  nor nor_1 (nor_1_out, and_5_out, and_6_out, and_7_out);
  and and_9 (Overflow, or_1_out, nor_1_out);

  assign b[4:3] = a[1:0];

  // Notes on the sheet:
  //   Douglas de Loredo Borges - 417889
endmodule

module Logic_Comparator_5_Bits (
  input  [4:0] a,
  input  [4:0] b,
  output a___b,
  output a____b
);

  wire xnor_1_out, xnor_2_out, xnor_3_out, xnor_4_out, xnor_5_out;

  xnor xnor_1 (xnor_1_out, b[0], a[0]);
  xnor xnor_2 (xnor_2_out, a[1], b[1]);
  xnor xnor_3 (xnor_3_out, a[2], b[2]);
  xnor xnor_4 (xnor_4_out, a[3], b[3]);
  xnor xnor_5 (xnor_5_out, a[4], b[4]);
  and and_1 (a___b, xnor_1_out, xnor_2_out, xnor_3_out, xnor_4_out, xnor_5_out);
  not not_1 (a____b, a___b);

  // Notes on the sheet:
  //   Douglas de Loredo Borges - 417889
endmodule

module Aritmetic_Comparator_5_Bits (
  input  [4:0] a,
  input  [4:0] b,
  input  a___b,
  input  [5:0] a___b_2,
  output a___b_3,
  output b___a
);

  wire and_1_out, and_2_out, and_3_out, not_1_out, not_2_out, undriven;

  and and_1 (and_1_out, undriven, not_1_out);
  not not_1 (not_1_out, a[1]);
  and and_2 (and_2_out, undriven, a___b_2[5]);
  not not_2 (not_2_out, a[1]);
  and and_3 (and_3_out, not_2_out, a___b_2[5]);
  or or_1 (b___a, and_1_out, and_2_out, and_3_out);
  nor nor_1 (a___b_3, a___b, b___a);

  assign b[4:3] = a[1:0];

  // Notes on the sheet:
  //   Douglas de Loredo Borges - 417889
endmodule

module Logical_AND (
  input  [4:0] a,
  input  [4:0] b,
  output [4:0] a___b
);

  and and_1 (a___b[0], a[0], b[0]);
  and and_2 (a___b[1], a[1], b[1]);
  and and_3 (a___b[2], a[2], b[2]);
  and and_4 (a___b[3], a[3], b[3]);
  and and_5 (a___b[4], a[4], b[4]);

  // Notes on the sheet:
  //   Douglas de Loredo Borges - 417889
endmodule

module Logical_OR (
  input  [4:0] a,
  input  [4:0] b,
  output [4:0] a___b
);

  or or_1 (a___b[0], a[0], b[0]);
  or or_2 (a___b[1], a[1], b[1]);
  or or_3 (a___b[2], a[2], b[2]);
  or or_4 (a___b[3], a[3], b[3]);
  or or_5 (a___b[4], a[4], b[4]);

  // Notes on the sheet:
  //   Douglas de Loredo Borges - 417889
endmodule

module _1_s_Complement (
  input  [4:0] a,
  output [4:0] Complemento_de_1
);

  not not_1 (Complemento_de_1[0], a[0]);
  not not_2 (Complemento_de_1[1], a[1]);
  not not_3 (Complemento_de_1[2], a[2]);
  not not_4 (Complemento_de_1[3], a[3]);
  not not_5 (Complemento_de_1[4], a[4]);

  // Notes on the sheet:
  //   Douglas de Loredo Borges - 417889
endmodule

module Operation_Selector (
  input  [3:0] Select,
  output Mux1,
  output Mux2,
  output Mux3_2,
  output Mux3_1,
  output Mux3_0,
  output Mux4_1,
  output Mux4_0,
  output Mux5,
  output Mux6
);

  wire and_2_out, and_3_out, and_4_out, and_5_out, and_6_out, and_7_out, not_1_out, not_2_out, not_3_out;

  not not_1 (not_1_out, Select[1]);
  not not_2 (not_2_out, Select[2]);
  not not_3 (not_3_out, Select[1]);
  and and_1 (Mux3_2, Select[3], Select[2]);
  and and_2 (and_2_out, Select[3], Select[1]);
  and and_3 (and_3_out, Select[3], not_1_out);
  and and_4 (and_4_out, Select[1], Select[0]);
  and and_5 (and_5_out, Select[2], Select[1]);
  and and_6 (and_6_out, not_2_out, not_3_out);
  and and_7 (and_7_out, Select[3], Select[2], Select[0]);
  or or_1 (Mux3_1, Mux3_2, and_2_out);
  or or_2 (Mux3_0, and_3_out, and_4_out, and_5_out);
  or or_3 (Mux5, and_6_out, and_7_out);
  or or_4 (Mux6, Select[3], Select[2]);

  assign Mux1 = Select[0];
  assign Mux2 = Select[0];
  assign Mux4_0 = Select[0];
  assign Mux4_1 = Select[1];

  // Notes on the sheet:
  //   Douglas de Loredo Borges - 417889
endmodule

module ALU_5_Bits (
  input  [4:0] a,
  input  [4:0] b,
  input  [3:0] Select,
  output [4:0] Resultado,
  output Sinal,
  output Overflow,
  output a___b,
  output b___a,
  output a___b_2,
  output a____b,
  output Zero,
  output Carry
);

  wire operation_selector_1_mux1, operation_selector_1_mux2, operation_selector_1_mux5,
       operation_selector_1_mux6;
  wire [1:0] operation_selector_1_mux4_0;
  wire [2:0] operation_selector_1_mux3_0;
  wire [4:0] logical_and_1_a___b, logical_or_1_a___b, multiplexer_1_out, multiplexer_2_out,
       multiplexer_3_out, multiplexer_5_out, n1_s_complement_1_complemento_de_1,
       n1_s_complement_2_complemento_de_1, n1_s_complement_3_complemento_de_1;
  wire [5:0] full_adder_5_bits_1_soma, \full_subtractor_5_bits_1_diferença ,
       \full_subtractor_5_bits_2_diferença ;
  wire [9:0] multiplexer_4_out;

  Logical_AND logical_and_1 (.a___b(logical_and_1_a___b), .a(a), .b(b));
  Logical_OR logical_or_1 (.a___b(logical_or_1_a___b), .a(a), .b(b));
  _1_s_Complement u_1_s_complement_1 (.Complemento_de_1(n1_s_complement_1_complemento_de_1), .a(a));
  _1_s_Complement u_1_s_complement_2 (.Complemento_de_1(n1_s_complement_2_complemento_de_1), .a(b));
  Multiplexer #(.width(5)) multiplexer_1 (.in0(a), .in1(b), .out(multiplexer_1_out), .sel(operation_selector_1_mux2));
  _1_s_Complement u_1_s_complement_3 (.Complemento_de_1(n1_s_complement_3_complemento_de_1), .a(multiplexer_1_out));
  Multiplexer #(.width(5)) multiplexer_2 (.in0(a), .in1(b), .out(multiplexer_2_out), .sel(operation_selector_1_mux1));
  Multiplexer #(.select(2), .width(5)) multiplexer_3 (
    .in0(logical_and_1_a___b), .in1(logical_or_1_a___b), .in2(n1_s_complement_1_complemento_de_1),
    .in3(n1_s_complement_2_complemento_de_1), .out(multiplexer_3_out), .sel(operation_selector_1_mux4_0));
  Multiplexer #(.select(3), .width(10)) multiplexer_4 (
    .in0({5'b00001, n1_s_complement_3_complemento_de_1}), .in1({5'b00001, multiplexer_2_out}), .in2({a, a}),
    .in3({b, b}), .in7({b, a}), .out(multiplexer_4_out), .sel(operation_selector_1_mux3_0));  // open: in4, in5, in6
  Operation_Selector operation_selector_1 (
    .Mux1(operation_selector_1_mux1), .Mux2(operation_selector_1_mux2),
    .Mux3_1(operation_selector_1_mux3_0[1]), .Mux3_0(operation_selector_1_mux3_0[0]),
    .Mux4_1(operation_selector_1_mux4_0[1]), .Mux4_0(operation_selector_1_mux4_0[0]),
    .Mux5(operation_selector_1_mux5), .Mux6(operation_selector_1_mux6), .Select(Select),
    .Mux3_2(operation_selector_1_mux3_0[2]));
  Full_Adder_5_Bits full_adder_5_bits_1 (
    .Soma(full_adder_5_bits_1_soma), .a(multiplexer_4_out[4:0]), .b(multiplexer_4_out[9:5]));
  Full_Subtractor_5_Bits full_subtractor_5_bits_1 (
    .\Diferença (\full_subtractor_5_bits_1_diferença ), .a(multiplexer_4_out[4:0]), .b(multiplexer_4_out[9:5]));
  Full_Subtractor_5_Bits full_subtractor_5_bits_2 (.\Diferença (\full_subtractor_5_bits_2_diferença ), .a(a), .b(b));
  Multiplexer #(.width(6)) multiplexer_5 (
    .in0(full_adder_5_bits_1_soma), .in1(\full_subtractor_5_bits_1_diferença ),
    .out({Carry, multiplexer_5_out}), .sel(operation_selector_1_mux5));
  Signal_Flag_5_Bits signal_flag_5_bits_1 (
    .Select(Select), .a(a), .b(b), .Op(operation_selector_1_mux5), .a_b___a_b({Carry, multiplexer_5_out}),
    .Sinal(Sinal));
  Overflow_Flag_5_Bits overflow_flag_5_bits_1 (
    .a(a), .b(b), .Op(operation_selector_1_mux5), .a_b___a_b({Carry, multiplexer_5_out}), .Select(Select),
    .Overflow(Overflow));
  Aritmetic_Comparator_5_Bits aritmetic_comparator_5_bits_1 (
    .b___a(b___a), .a(a), .b(b), .a___b_2(\full_subtractor_5_bits_2_diferença ), .a___b(a___b_2),
    .a___b_3(a___b));
  Logic_Comparator_5_Bits logic_comparator_5_bits_1 (.a___b(a___b_2), .a(b), .b(a), .a____b(a____b));
  Multiplexer #(.width(5)) multiplexer_6 (
    .in0(multiplexer_3_out), .in1({Sinal, multiplexer_5_out[3:0]}), .out(Resultado),
    .sel(operation_selector_1_mux6));
  nor nor_1 (Zero, Resultado[0], Resultado[1], Resultado[2], Resultado[3], Resultado[4], Carry);

  // Notes on the sheet:
  //   2
  //   1
  //   4
  //   Douglas de Loredo Borges - 417889
  //   3
  //   5
  //   6
endmodule
