// Logisim project guia6.circ as structural Verilog
module meia_soma_01 (
  input  e1,
  input  e2,
  output soma,
  output carry
);

  xor xor_1 (soma, e2, e1);
  and and_1 (carry, e1, e2);

  // Notes on the sheet:
  //   Isabella Gonçales - 420120
endmodule

module soma_completa_01 (
  input  e1,
  input  e2,
  input  e3,
  output carry_out,
  output soma
);

  wire meia_soma_01_1_carry, meia_soma_01_1_soma, meia_soma_01_2_carry;

  meia_soma_01 meia_soma_01_1 (.e1(e1), .e2(e2), .soma(meia_soma_01_1_soma), .carry(meia_soma_01_1_carry));
  meia_soma_01 meia_soma_01_2 (.e1(meia_soma_01_1_soma), .e2(e3), .soma(soma), .carry(meia_soma_01_2_carry));
  or or_1 (carry_out, meia_soma_01_1_carry, meia_soma_01_2_carry);

  // Notes on the sheet:
  //   Isabella Gonçales - 420120
endmodule

module Somador_5Bits_01 (
  input  [4:0] e1,
  input  [4:0] e2,
  output carry,
  output [4:0] somas
);

  wire meia_soma_01_1_carry, soma_completa_01_2_carry_out, soma_completa_01_3_carry_out,
       soma_completa_01_4_carry_out;

  soma_completa_01 soma_completa_01_1 (
    .e1(e1[4]), .e2(e2[4]), .e3(soma_completa_01_2_carry_out), .carry_out(carry), .soma(somas[4]));
  soma_completa_01 soma_completa_01_2 (
    .e1(e1[3]), .e2(e2[3]), .e3(soma_completa_01_3_carry_out), .carry_out(soma_completa_01_2_carry_out),
    .soma(somas[3]));
  soma_completa_01 soma_completa_01_3 (
    .e1(e1[2]), .e2(e2[2]), .e3(soma_completa_01_4_carry_out), .carry_out(soma_completa_01_3_carry_out),
    .soma(somas[2]));
  soma_completa_01 soma_completa_01_4 (
    .e1(e1[1]), .e2(e2[1]), .e3(meia_soma_01_1_carry), .carry_out(soma_completa_01_4_carry_out),
    .soma(somas[1]));
  meia_soma_01 meia_soma_01_1 (.e1(e1[0]), .e2(e2[0]), .soma(somas[0]), .carry(meia_soma_01_1_carry));

  // Notes on the sheet:
  //   Isabella Gonçales - 420120 
endmodule

module Comparador_01 (
  input  [3:0] e1,
  input  [3:0] e2,
  output a___b,
  output a____b
);

  wire xnor_1_out, xnor_2_out, xnor_3_out, xnor_4_out;

  xnor xnor_1 (xnor_1_out, e2[0], e1[0]);
  xnor xnor_2 (xnor_2_out, e2[1], e1[1]);
  xnor xnor_3 (xnor_3_out, e2[2], e1[2]);
  xnor xnor_4 (xnor_4_out, e2[3], e1[3]);
  and and_1 (a___b, xnor_1_out, xnor_2_out, xnor_3_out, xnor_4_out);
  not not_1 (a____b, a___b);

  // Notes on the sheet:
  //   Isabella Gonçales - 420120
endmodule

module \meia_diferença_02  (
  input  e1,
  input  e2,
  output \diferença ,
  output sinal
);

  wire not_1_out;

  xor xor_1 (\diferença , e1, e2);
  not not_1 (not_1_out, e1);
  and and_1 (sinal, e2, not_1_out);

  // Notes on the sheet:
  //   Isabella Gonçales - 420120
endmodule

module \diferença_completa_02  (
  input  e1,
  input  e2,
  input  e3,
  output sinal,
  output \diferença 
);

  wire \meia_diferença_02_1_diferença , \meia_diferença_02_1_sinal , \meia_diferença_02_2_sinal ;

  \meia_diferença_02  \meia_diferença_02_1  (
    .e1(e1), .e2(e2), .\diferença (\meia_diferença_02_1_diferença ), .sinal(\meia_diferença_02_1_sinal ));
  \meia_diferença_02  \meia_diferença_02_2  (
    .e1(\meia_diferença_02_1_diferença ), .e2(e3), .\diferença (\diferença ),
    .sinal(\meia_diferença_02_2_sinal ));
  or or_1 (sinal, \meia_diferença_02_1_sinal , \meia_diferença_02_2_sinal );

  // Notes on the sheet:
  //   temp1
  //   temp2
  //   Isabella Gonçales - 420120
  //   temp3
endmodule

module \Diferença_5Bits  (
  input  [4:0] e1,
  input  [4:0] e2,
  output out_3,
  output [4:0] \Diferenças 
);

  wire \diferença_completa_02_2_sinal , \diferença_completa_02_3_sinal , \diferença_completa_02_4_sinal ,
       \meia_diferença_02_1_sinal ;

  \diferença_completa_02  \diferença_completa_02_1  (
    .e1(e1[4]), .e2(e2[4]), .e3(\diferença_completa_02_2_sinal ), .sinal(out_3), .\diferença (\Diferenças [4]));
  \diferença_completa_02  \diferença_completa_02_2  (
    .e1(e1[3]), .e2(e2[3]), .e3(\diferença_completa_02_3_sinal ), .sinal(\diferença_completa_02_2_sinal ),
    .\diferença (\Diferenças [3]));
  \diferença_completa_02  \diferença_completa_02_3  (
    .e1(e1[2]), .e2(e2[2]), .e3(\diferença_completa_02_4_sinal ), .sinal(\diferença_completa_02_3_sinal ),
    .\diferença (\Diferenças [2]));
  \diferença_completa_02  \diferença_completa_02_4  (
    .e1(e1[1]), .e2(e2[1]), .e3(\meia_diferença_02_1_sinal ), .sinal(\diferença_completa_02_4_sinal ),
    .\diferença (\Diferenças [1]));
  \meia_diferença_02  \meia_diferença_02_1  (
    .e1(e1[0]), .e2(e2[0]), .\diferença (\Diferenças [0]), .sinal(\meia_diferença_02_1_sinal ));

  // Notes on the sheet:
  //   Isabella Gonçales - 420120
endmodule

module Comparador_02 (
  input  [4:0] a___b,
  input  a___b_2,
  output b___a,
  output a___b_3
);

  nor nor_1 (a___b_3, a___b[4], a___b_2);

  assign b___a = a___b[4];

  // Notes on the sheet:
  //   Isabella Gonçales - 420120 
endmodule

module Sinal_Overflow_Zero (
  input  [3:0] in_1,
  input  in_2
);

  // AND_Gate and_1 has open pins: in3=in_1[3], out=open
endmodule
