// Logisim project Guia7Exe.circ as structural Verilog: 5 circuits, main circuit CircuitoExec
module CircuitoExec (
  input  a4,
  input  a3,
  input  a2,
  input  a1,
  input  a0,
  input  in_6,
  input  in_7,
  output s0,
  output s1,
  output s2,
  output s3,
  output s4,
  output w0,
  output w1,
  output w2,
  output w3,
  output w4,
  output w5,
  output z0,
  output z1,
  output z2,
  output z4,
  output z5
);

  Complemento1 complemento1_1 (
    .a0(a0), .a1(a1), .a2(a2), .a3(a3), .a4(a4), .s0(s0), .s1(s1), .s2(s2), .s3(s3), .s4(s4));
  Complemento2 complemento2_1 (
    .Key(in_6), .a0(a0), .a1(a1), .a2(a2), .a3(a3), .a4(a4), .s0(w0), .s1(w1), .s2(w2), .s3(w3), .s4(w4),
    .s5(w5));
  // Incremento1 incremento1_1: pin names not known; wires that end beside it: in_7, a0, a1, a2, a3, a4, z0, z1, z2, z4, z5

  // Notes on the sheet:
  //    Marden Batista , Matricula 388613
  //   Entradas
endmodule

module Complemento1 (
  input  a0,
  input  a1,
  input  a2,
  input  a3,
  input  a4,
  output s0,
  output s1,
  output s2,
  output s3,
  output s4
);

  not not_1 (s0, a0);
  not not_2 (s1, a1);
  not not_3 (s2, a2);
  not not_4 (s3, a3);
  not not_5 (s4, a4);
endmodule

module MeiaSoma (
  input  a,
  input  b,
  output s0,
  output s1
);

  xor xor_1 (s0, a, b);
  and and_1 (s1, a, b);
endmodule

module Complemento2 (
  input  Key,
  input  a0,
  input  a1,
  input  a2,
  input  a3,
  input  a4,
  output s0,
  output s1,
  output s2,
  output s3,
  output s4,
  output s5
);

  wire meiasoma_1_s1, meiasoma_2_s1, meiasoma_3_s1, meiasoma_4_s1, not_1_out, not_2_out, not_3_out,
       not_4_out, not_5_out;

  MeiaSoma meiasoma_1 (.a(Key), .b(not_1_out), .s0(s0), .s1(meiasoma_1_s1));
  not not_1 (not_1_out, a0);
  MeiaSoma meiasoma_2 (.a(meiasoma_1_s1), .b(not_2_out), .s0(s1), .s1(meiasoma_2_s1));
  not not_2 (not_2_out, a1);
  MeiaSoma meiasoma_3 (.a(meiasoma_2_s1), .b(not_3_out), .s0(s2), .s1(meiasoma_3_s1));
  not not_3 (not_3_out, a2);
  MeiaSoma meiasoma_4 (.a(meiasoma_3_s1), .b(not_4_out), .s0(s3), .s1(meiasoma_4_s1));
  not not_4 (not_4_out, a3);
  MeiaSoma meiasoma_5 (.a(meiasoma_4_s1), .b(not_5_out), .s0(s4), .s1(s5));
  not not_5 (not_5_out, a4);
endmodule

module Incremento1 (
  input  Key,
  input  a0,
  input  a1,
  input  a2,
  input  a3,
  input  a4,
  output s0,
  output s1,
  output s2,
  output s3,
  output s4,
  output s5
);

  wire meiasoma_1_s1, meiasoma_2_s1, meiasoma_3_s1, meiasoma_4_s1;

  MeiaSoma meiasoma_1 (.a(Key), .b(a0), .s0(s0), .s1(meiasoma_1_s1));
  MeiaSoma meiasoma_2 (.a(meiasoma_1_s1), .b(a1), .s0(s1), .s1(meiasoma_2_s1));
  MeiaSoma meiasoma_3 (.a(meiasoma_2_s1), .b(a2), .s0(s2), .s1(meiasoma_3_s1));
  MeiaSoma meiasoma_4 (.a(meiasoma_3_s1), .b(a3), .s0(s3), .s1(meiasoma_4_s1));
  MeiaSoma meiasoma_5 (.a(meiasoma_4_s1), .b(a4), .s0(s4), .s1(s5));
endmodule
