// Logisim project Guia_07.circ as structural Verilog: 15 circuits, main circuit Half Adder
// HA
module Half_Adder (
  input  A,
  input  B,
  output s1,
  output s0
);

  wire nor_1_out, nor_2_out, nor_3_out, nor_4_out, nor_5_out, nor_6_out, nor_8_out;

  nor nor_1 (nor_1_out, A, A);
  nor nor_2 (nor_2_out, B, B);
  nor nor_3 (nor_3_out, A, A);
  nor nor_4 (nor_4_out, B, B);
  nor nor_5 (nor_5_out, nor_3_out, B);
  nor nor_6 (nor_6_out, nor_4_out, A);
  nor nor_7 (s1, nor_1_out, nor_2_out);
  nor nor_8 (nor_8_out, nor_5_out, nor_6_out);
  nor nor_9 (s0, nor_8_out, nor_8_out);

  // Notes on the sheet:
  //   Aluno: Alyson Deives
  //   Matricula: 416589
  //   Guia 04_01 - Half Adder with NOR gates
endmodule

// FA
module Full_Adder (
  input  A,
  input  B,
  input  C,
  output s1,
  output s0
);

  wire half_adder_1_s0, half_adder_1_s1, half_adder_2_s1;

  Half_Adder half_adder_1 (.A(B), .B(A), .s1(half_adder_1_s1), .s0(half_adder_1_s0));
  Half_Adder half_adder_2 (.A(C), .B(half_adder_1_s0), .s1(half_adder_2_s1), .s0(s0));
  or or_1 (s1, half_adder_1_s1, half_adder_2_s1);

  // Notes on the sheet:
  //   Aluno: Alyson Deives
  //   Matricula: 416589
  //   Guia 04_02 - Full Adder with NOR gates
endmodule

// HS
module Half_Subtractor (
  input  A,
  input  B,
  output s1,
  output s0
);

  wire nor_1_out, nor_2_out, nor_3_out, nor_4_out, nor_5_out, nor_7_out;

  nor nor_1 (nor_1_out, B, B);
  nor nor_2 (nor_2_out, A, A);
  nor nor_3 (nor_3_out, B, B);
  nor nor_4 (nor_4_out, nor_2_out, B);
  nor nor_5 (nor_5_out, nor_3_out, A);
  nor nor_6 (s1, A, nor_1_out);
  nor nor_7 (nor_7_out, nor_4_out, nor_5_out);
  nor nor_8 (s0, nor_7_out, nor_7_out);

  // Notes on the sheet:
  //   Aluno: Alyson Deives
  //   Matricula: 416589
  //   Guia 03_05 - Half Differ with NOR gates
endmodule

// FS
module Full_Subtractor (
  input  A,
  input  B,
  input  C,
  output s1,
  output s0
);

  wire half_subtractor_1_s0, half_subtractor_1_s1, half_subtractor_2_s1;

  Half_Subtractor half_subtractor_1 (.A(A), .B(B), .s1(half_subtractor_1_s1), .s0(half_subtractor_1_s0));
  Half_Subtractor half_subtractor_2 (.A(half_subtractor_1_s0), .B(C), .s1(half_subtractor_2_s1), .s0(s0));
  or or_1 (s1, half_subtractor_1_s1, half_subtractor_2_s1);

  // Notes on the sheet:
  //   Aluno: Alyson Deives
  //   Matricula: 416589
  //   Guia 04_03 - Half Differ with NOR gates
endmodule

module _4bits_Adder (
  input  a3,
  input  a2,
  input  a1,
  input  a0,
  input  b3,
  input  b2,
  input  b1,
  input  b0,
  output s3,
  output s2,
  output s1,
  output s0,
  output OVERFLOW
);

  wire full_adder_2_s1, full_adder_3_s1, half_adder_1_s1;

  Full_Adder full_adder_1 (.A(a3), .B(b3), .C(full_adder_2_s1), .s1(OVERFLOW), .s0(s3));
  Full_Adder full_adder_2 (.A(a2), .B(b2), .C(full_adder_3_s1), .s1(full_adder_2_s1), .s0(s2));
  Full_Adder full_adder_3 (.A(a1), .B(b1), .C(half_adder_1_s1), .s1(full_adder_3_s1), .s0(s1));
  Half_Adder half_adder_1 (.A(a0), .B(b0), .s1(half_adder_1_s1), .s0(s0));

  // Notes on the sheet:
  //   Matricula: 416589
  //   Guia 05_01 - Full Adder 4 bits
  //   Aluno: Alyson Deives
endmodule

// 4bits_Subtr
module _4bits_Subtractor (
  input  a3,
  input  a2,
  input  a1,
  input  a0,
  input  b3,
  input  b2,
  input  b1,
  input  b0,
  output CARRY,
  output s3,
  output s3_2,
  output s1,
  output s0
);

  wire full_subtractor_2_s1, full_subtractor_3_s1, half_subtractor_1_s1;

  Full_Subtractor full_subtractor_1 (.A(a3), .B(b3), .C(full_subtractor_2_s1), .s1(CARRY), .s0(s3));
  Full_Subtractor full_subtractor_2 (.A(a2), .B(b2), .C(full_subtractor_3_s1), .s1(full_subtractor_2_s1), .s0(s3_2));
  Full_Subtractor full_subtractor_3 (.A(a1), .B(b1), .C(half_subtractor_1_s1), .s1(full_subtractor_3_s1), .s0(s1));
  Half_Subtractor half_subtractor_1 (.A(a0), .B(b0), .s1(half_subtractor_1_s1), .s0(s0));

  // Notes on the sheet:
  //   Guia 05_02 - Full Subtractor 3 bits
  //   Aluno: Alyson Deives
  //   Matricula: 416589
endmodule

module _3bits_Multiplier (
  input  a2,
  input  a1,
  input  a0,
  input  b2,
  input  b1,
  input  b0,
  output s0,
  output s5,
  output s4,
  output s3,
  output s2,
  output s1
);

  wire and_2_out, and_3_out, and_4_out, and_5_out, and_6_out, and_7_out, and_8_out, and_9_out,
       n4bits_adder_1_s0, n4bits_adder_1_s1, n4bits_adder_1_s2, n4bits_adder_1_s3;

  and and_1 (s0, a0, b0);
  and and_2 (and_2_out, a1, b0);
  and and_3 (and_3_out, a2, b0);
  and and_4 (and_4_out, a0, b1);
  and and_5 (and_5_out, a1, b1);
  and and_6 (and_6_out, a2, b1);
  and and_7 (and_7_out, a0, b2);
  and and_8 (and_8_out, a1, b2);
  and and_9 (and_9_out, a2, b2);
  _4bits_Adder u_4bits_adder_1 (
    .a3(1'b0), .b3(1'b0), .a2(and_6_out), .b2(1'b0), .a1(and_5_out), .b1(and_3_out), .a0(and_4_out),
    .b0(and_2_out), .s3(n4bits_adder_1_s3), .s2(n4bits_adder_1_s2), .s1(n4bits_adder_1_s1),
    .s0(n4bits_adder_1_s0));  // open: OVERFLOW
  _4bits_Adder u_4bits_adder_2 (
    .a3(and_9_out), .OVERFLOW(s5), .b3(n4bits_adder_1_s3), .a2(and_8_out), .b2(n4bits_adder_1_s2),
    .a1(and_7_out), .b1(n4bits_adder_1_s1), .a0(1'b0), .b0(n4bits_adder_1_s0), .s3(s4), .s2(s3), .s1(s2),
    .s0(s1));

  // Notes on the sheet:
  //   Guia 05_03 - Multiplier 3 bits
  //   Aluno: Alyson Deives
  //   Matricula: 416589
endmodule

module ALU (
  input  Op,
  input  a3,
  input  a2,
  input  a1,
  input  a0,
  input  b3,
  input  b2,
  input  b1,
  input  b0,
  output OVERFLOW___CARRY,
  output SINAL,
  output s3,
  output s2,
  output s1,
  output s0,
  output a_b,
  output b_a,
  output A____B,
  output s3_2,
  output s2_2,
  output s1_2,
  output s0_2,
  output s3_3,
  output s2_3,
  output s1_3,
  output s0_3,
  output s3_4,
  output s2_4,
  output s1_4,
  output s0_4,
  output s3_5,
  output s3_6,
  output s2_5,
  output s1_5,
  output s0_5,
  output s3_7,
  output s3_8,
  output s2_6,
  output s1_6,
  output s0_6
);

  wire and_1_out, and_2_out, and_3_out, and_4_out, and_5_out, and_6_out, and_7_out, and_8_out, and_9_out,
       and_10_out, and_11_out, and_12_out, and_13_out, and_14_out, and_15_out, and_16_out, n4bits_adder_1_s0,
       n4bits_adder_1_s1, n4bits_adder_1_s2, n4bits_adder_1_s3, n4bits_subtractor_1_s0,
       n4bits_subtractor_1_s1, n4bits_subtractor_1_s3, n4bits_subtractor_1_s3_2, not_1_out;

  x2 x2_1 (.a3(a3), .a2(a2), .a1(a1), .a0(a0), .s3(s3_7), .s3_2(s3_8), .s2(s2_6), .s1(s1_6), .s0(s0_6));
  _1_2 u_1_1 (.a3(a3), .a2(a2), .a1(a1), .a0(a0), .s3(s3_5), .s3_2(s3_6), .s2(s2_5), .s1(s1_5), .s0(s0_5));
  _1 u_1_2 (.a3(a3), .a2(a2), .a1(a1), .a0(a0), .s3(s3_4), .s2(s2_4), .s1(s1_4), .s0(s0_4));
  C2 c2_1 (.a3(a3), .a2(a2), .a1(a1), .a0(a0), .s3(s3_3), .s2(s2_3), .s1(s1_3), .s0(s0_3));
  C1 c1_1 (.a3(a3), .a2(a2), .a1(a1), .a0(a0), .s3(s3_2), .s2(s2_2), .s1(s1_2), .s0(s0_2));
  Logic_Comparator logic_comparator_1 (
    .a3(a3), .b3(b3), .a2(a2), .b2(b2), .a1(a1), .b1(b1), .a0(a0), .b0(b0), .s0(A____B));
  and and_1 (and_1_out, a3, not_1_out);
  and and_2 (and_2_out, a2, not_1_out);
  and and_3 (and_3_out, a1, not_1_out);
  and and_4 (and_4_out, a0, not_1_out);
  and and_5 (and_5_out, b3, not_1_out);
  _4bits_Adder u_4bits_adder_1 (
    .a3(and_1_out), .OVERFLOW(OVERFLOW___CARRY), .b3(and_5_out), .a2(and_2_out), .b2(and_7_out),
    .a1(and_3_out), .b1(and_6_out), .a0(and_4_out), .b0(and_8_out), .s3(n4bits_adder_1_s3),
    .s2(n4bits_adder_1_s2), .s1(n4bits_adder_1_s1), .s0(n4bits_adder_1_s0));
  or or_1 (s3, n4bits_adder_1_s3, n4bits_subtractor_1_s3);
  and and_6 (and_6_out, b1, not_1_out);
  and and_7 (and_7_out, b2, not_1_out);
  or or_2 (s2, n4bits_adder_1_s2, n4bits_subtractor_1_s3_2);
  or or_3 (s1, n4bits_adder_1_s1, n4bits_subtractor_1_s1);
  and and_8 (and_8_out, b0, not_1_out);
  or or_4 (s0, n4bits_adder_1_s0, n4bits_subtractor_1_s0);
  and and_9 (and_9_out, a3, Op);
  and and_10 (and_10_out, a2, Op);
  and and_11 (and_11_out, a0, Op);
  and and_12 (and_12_out, a1, Op);
  _4bits_Subtractor u_4bits_subtractor_1 (
    .a3(and_9_out), .b3(and_14_out), .a2(and_10_out), .b2(and_13_out), .a1(and_12_out), .b1(and_15_out),
    .a0(and_11_out), .b0(and_16_out), .CARRY(b_a), .s3(n4bits_subtractor_1_s3),
    .s3_2(n4bits_subtractor_1_s3_2), .s1(n4bits_subtractor_1_s1), .s0(n4bits_subtractor_1_s0));
  nor nor_1 (a_b, A____B, b_a);
  and and_13 (and_13_out, b2, Op);
  and and_14 (and_14_out, b3, Op);
  not not_1 (not_1_out, Op);
  and and_15 (and_15_out, b1, Op);
  and and_16 (and_16_out, b0, Op);

  assign SINAL = b_a;

  // Notes on the sheet:
  //   -1
  //   x2
  //   C1
  //   C2
  //   +1
  //   Guia 07 - ALU
  //   Aluno: Alyson Deives
  //   Matricula: 416589
endmodule

// LC
module Logic_Comparator (
  input  a3,
  input  a2,
  input  a1,
  input  a0,
  input  b3,
  input  b2,
  input  b1,
  input  b0,
  output s0
);

  wire xnor_1_out, xnor_2_out, xnor_3_out, xnor_4_out;

  xnor xnor_1 (xnor_1_out, a3, b3);
  xnor xnor_2 (xnor_2_out, a2, b2);
  xnor xnor_3 (xnor_3_out, a1, b1);
  and and_1 (s0, xnor_1_out, xnor_2_out, xnor_3_out, xnor_4_out);
  xnor xnor_4 (xnor_4_out, a0, b0);
endmodule

module Arithmetic_Comparator (
  input  a3,
  input  a2,
  input  a1,
  input  a0,
  input  b3,
  input  b2,
  input  b1,
  input  b0,
  output a_b,
  output a__b,
  output a_b_2
);

  wire and_1_out, and_2_out, and_3_out, and_5_out, and_6_out, and_7_out, and_8_out, and_9_out, not_1_out,
       not_2_out, not_3_out, not_4_out, not_5_out, not_6_out, not_8_out, not_9_out, not_10_out, or_1_out;

  not not_1 (not_1_out, b3);
  not not_2 (not_2_out, b2);
  and and_1 (and_1_out, a3, not_1_out);
  and and_2 (and_2_out, a2, not_2_out);
  not not_3 (not_3_out, b1);
  and and_3 (and_3_out, a1, not_3_out);
  or or_1 (or_1_out, and_1_out, and_2_out, and_3_out, and_5_out);
  not not_4 (not_4_out, a_b_2);
  and and_4 (a_b, or_1_out, not_4_out);
  not not_5 (not_5_out, b0);
  not not_6 (not_6_out, a3);
  and and_5 (and_5_out, a0, not_5_out);
  and and_6 (and_6_out, not_6_out, b3);
  not not_7 (a__b, or_1_out);
  not not_8 (not_8_out, a2);
  and and_7 (and_7_out, not_8_out, b2);
  or or_2 (a_b_2, and_6_out, and_7_out, and_8_out, and_9_out);
  not not_9 (not_9_out, a0);
  not not_10 (not_10_out, a1);
  and and_8 (and_8_out, not_10_out, b1);
  and and_9 (and_9_out, not_9_out, b0);
endmodule

module C1 (
  input  a3,
  input  a2,
  input  a1,
  input  a0,
  output s3,
  output s2,
  output s1,
  output s0
);

  not not_1 (s3, a3);
  not not_2 (s2, a2);
  not not_3 (s1, a1);
  not not_4 (s0, a0);

  // Notes on the sheet:
  //   Matricula: 416589
  //   Guia 07_01 - Complemento de 1
  //   Aluno: Alyson Deives
endmodule

module C2 (
  input  a3,
  input  a2,
  input  a1,
  input  a0,
  output s3,
  output s2,
  output s1,
  output s0
);

  wire c1_1_s0, c1_1_s1, c1_1_s2, c1_1_s3;

  C1 c1_1 (.a3(a3), .a2(a2), .a1(a1), .a0(a0), .s3(c1_1_s3), .s2(c1_1_s2), .s1(c1_1_s1), .s0(c1_1_s0));
  _4bits_Adder u_4bits_adder_1 (
    .a3(c1_1_s3), .b3(1'b0), .a2(c1_1_s2), .b2(1'b0), .a1(c1_1_s1), .b1(1'b0), .a0(c1_1_s0), .b0(1'b1),
    .s3(s3), .s2(s2), .s1(s1), .s0(s0));  // open: OVERFLOW

  // Notes on the sheet:
  //   Matricula: 416589
  //   Guia 07_02 - Complemento de 2
  //   Aluno: Alyson Deives
endmodule

module _1 (
  input  a3,
  input  a2,
  input  a1,
  input  a0,
  output s3,
  output s2,
  output s1,
  output s0
);

  _4bits_Adder u_4bits_adder_1 (
    .a3(a3), .b3(1'b0), .a2(a2), .b2(1'b0), .a1(a1), .b1(1'b0), .a0(a0), .b0(1'b1), .s3(s3), .s2(s2),
    .s1(s1), .s0(s0));  // open: OVERFLOW

  // Notes on the sheet:
  //   Matricula: 416589
  //   Guia 07_03 - Incremento de 1
  //   Aluno: Alyson Deives
endmodule

module _1_2 (
  input  a3,
  input  a2,
  input  a1,
  input  a0,
  output s3,
  output s3_2,
  output s2,
  output s1,
  output s0
);

  _4bits_Subtractor u_4bits_subtractor_1 (
    .a3(a3), .b3(1'b0), .a2(a2), .b2(1'b0), .a1(a1), .b1(1'b0), .a0(a0), .b0(1'b1), .CARRY(s3), .s3(s3_2),
    .s3_2(s2), .s1(s1), .s0(s0));

  // Notes on the sheet:
  //   Aluno: Alyson Deives
  //   Matricula: 416589
  //   Guia 07_04 - Decremento de 1
endmodule

module x2 (
  input  a3,
  input  a2,
  input  a1,
  input  a0,
  output s3,
  output s3_2,
  output s2,
  output s1,
  output s0
);


  assign s0 = 1'b0;
  assign s1 = a0;
  assign s2 = a1;
  assign s3 = a3;
  assign s3_2 = a2;

  // Notes on the sheet:
  //   Aluno: Alyson Deives
  //   Matricula: 416589
  //   Guia 07_05 - Produto por 2
endmodule
