// Logisim project guia06.circ as structural Verilog: 10 circuits, main circuit MeioSomador
module ALU4_bits (
  input  [3:0] A,
  input  [3:0] B,
  input  [3:0] chave,
  output Carry,
  output Sinal,
  output [4:0] Saida
);

  wire [3:0] complementode1_1_complemento_de_1, complementode1_2_complemento_de_1;
  wire [4:0] comparador_1_comparador, somador4_bits_1_soma, somador4_bits_2_soma, somador4_bits_3_soma,
       subtrator4_bits_1_diferenca;

  Somador4_Bits somador4_bits_1 (.a(A), .b(B), .out_3(Carry), .Soma(somador4_bits_1_soma));
  Comparador comparador_1 (.a(A), .b(B), .Comparador(comparador_1_comparador[0]));
  Subtrator4_Bits subtrator4_bits_1 (.a(A), .b(B), .Sinal(Sinal), .Diferenca(subtrator4_bits_1_diferenca));
  Complementode1 complementode1_1 (.a(A), .Complemento_de_1(complementode1_1_complemento_de_1));
  Complementode1 complementode1_2 (.a(B), .Complemento_de_1(complementode1_2_complemento_de_1));
  Somador4_Bits somador4_bits_2 (
    .a(complementode1_1_complemento_de_1), .b(4'b0001), .Soma(somador4_bits_2_soma));  // open: out_3
  Somador4_Bits somador4_bits_3 (
    .a(complementode1_2_complemento_de_1), .b(4'b0001), .Soma(somador4_bits_3_soma));  // open: out_3
  \Comparador_aritmético  \comparador_aritmético_1  (.a___b(subtrator4_bits_1_diferenca));  // open: Comparador, a_b, a_b_2
  Multiplexer #(.select(4), .width(5)) multiplexer_1 (
    .in0(somador4_bits_1_soma), .in1(comparador_1_comparador), .in2(subtrator4_bits_1_diferenca),
    .in3({1'b0, complementode1_1_complemento_de_1}), .in4({1'b0, complementode1_2_complemento_de_1}),
    .in5(somador4_bits_2_soma), .in6(somador4_bits_3_soma), .out(Saida), .sel(chave));  // open: in7, in8, in9, in10, in11, in12, in13, in14, in15

  // Notes on the sheet:
  //   00-soma
  //   01 -comparador logico
  //   10-subtrator
  //   11-complemento de 1 a
  //   100-complemento de 1 b
  //   101-Complemento de 2 a
  //   110-Complemento de 2 b
endmodule

module MeioSomador (
  input  a,
  input  b,
  output Soma,
  output Carry
);

  and and_1 (Carry, b, a);
  xor xor_1 (Soma, a, b);

  // Notes on the sheet:
  //   Giselle Caroline Vieira
endmodule

module SomadorCompleto (
  input  a,
  input  b,
  input  c,
  output Soma,
  output CarryOut
);

  wire meiosomador_1_carry, meiosomador_1_soma, meiosomador_2_carry;

  MeioSomador meiosomador_1 (.a(a), .b(b), .Soma(meiosomador_1_soma), .Carry(meiosomador_1_carry));
  MeioSomador meiosomador_2 (.a(meiosomador_1_soma), .b(c), .Soma(Soma), .Carry(meiosomador_2_carry));
  or or_1 (CarryOut, meiosomador_2_carry, meiosomador_1_carry);
endmodule

module Somador4_Bits (
  input  [3:0] a,
  input  [3:0] b,
  output out_3,
  output [4:0] Soma
);

  wire meiosomador_1_carry, somadorcompleto_1_carryout, somadorcompleto_3_carryout;

  SomadorCompleto somadorcompleto_1 (
    .a(a[2]), .b(b[2]), .c(somadorcompleto_3_carryout), .Soma(Soma[2]), .CarryOut(somadorcompleto_1_carryout));
  SomadorCompleto somadorcompleto_2 (
    .a(a[3]), .b(b[3]), .c(somadorcompleto_1_carryout), .Soma(Soma[3]), .CarryOut(out_3));
  SomadorCompleto somadorcompleto_3 (
    .a(a[1]), .b(b[1]), .c(meiosomador_1_carry), .Soma(Soma[1]), .CarryOut(somadorcompleto_3_carryout));
  MeioSomador meiosomador_1 (.a(a[0]), .b(b[0]), .Soma(Soma[0]), .Carry(meiosomador_1_carry));

  assign Soma[4] = out_3;
endmodule

module MeioSubtrator (
  input  a,
  input  b,
  output diferenca,
  output Sinal
);

  wire not_1_out;

  not not_1 (not_1_out, a);
  xor xor_1 (diferenca, a, b);
  and and_1 (Sinal, not_1_out, b);
endmodule

module SubtratorCompleto (
  input  a,
  input  b,
  input  c,
  output diferenca,
  output Sinal
);

  wire meiosubtrator_1_diferenca, meiosubtrator_1_sinal, meiosubtrator_2_sinal;

  MeioSubtrator meiosubtrator_1 (.a(a), .b(b), .diferenca(meiosubtrator_1_diferenca), .Sinal(meiosubtrator_1_sinal));
  MeioSubtrator meiosubtrator_2 (
    .a(meiosubtrator_1_diferenca), .b(c), .diferenca(diferenca), .Sinal(meiosubtrator_2_sinal));
  or or_1 (Sinal, meiosubtrator_2_sinal, meiosubtrator_1_sinal);
endmodule

module Subtrator4_Bits (
  input  [3:0] a,
  input  [3:0] b,
  output Sinal,
  output [4:0] Diferenca
);

  wire meiosubtrator_1_sinal, subtratorcompleto_2_sinal, subtratorcompleto_3_sinal;

  SubtratorCompleto subtratorcompleto_1 (
    .a(a[3]), .b(b[3]), .c(subtratorcompleto_2_sinal), .diferenca(Diferenca[3]), .Sinal(Diferenca[4]));
  SubtratorCompleto subtratorcompleto_2 (
    .a(a[2]), .b(b[2]), .c(subtratorcompleto_3_sinal), .diferenca(Diferenca[2]),
    .Sinal(subtratorcompleto_2_sinal));
  SubtratorCompleto subtratorcompleto_3 (
    .a(a[1]), .b(b[1]), .c(meiosubtrator_1_sinal), .diferenca(Diferenca[1]), .Sinal(subtratorcompleto_3_sinal));
  MeioSubtrator meiosubtrator_1 (.a(a[0]), .b(b[0]), .diferenca(Diferenca[0]), .Sinal(meiosubtrator_1_sinal));

  assign Sinal = Diferenca[4];
endmodule

module Comparador (
  input  [3:0] a,
  input  [3:0] b,
  output Comparador
);

  wire xor_1_out, xor_2_out, xor_3_out, xor_4_out;

  xor xor_1 (xor_1_out, b[3], a[3]);
  xor xor_2 (xor_2_out, b[2], a[2]);
  and and_1 (Comparador, xor_1_out, xor_2_out, xor_3_out, xor_4_out);
  xor xor_3 (xor_3_out, b[1], a[1]);
  xor xor_4 (xor_4_out, b[0], a[0]);
endmodule

module Complementode1 (
  input  [3:0] a,
  output [3:0] Complemento_de_1
);

  not not_1 (Complemento_de_1[0], a[0]);
  not not_2 (Complemento_de_1[1], a[1]);
  not not_3 (Complemento_de_1[2], a[2]);
  not not_4 (Complemento_de_1[3], a[3]);
endmodule

module \Comparador_aritmético  (
  input  [4:0] a___b,
  input  Comparador,
  output a_b,
  output a_b_2
);

  wire not_1_out;

  not not_1 (not_1_out, a___b[4]);
  and and_1 (a_b_2, not_1_out, Comparador);

  assign a_b = a___b[4];

  // Notes on the sheet:
  //   a<b
  //   a>b
endmodule
