// Logisim project Exercicio 01.circ as structural Verilog: 1 circuit, main circuit main
module main (
  input  a,
  input  b,
  input  c,
  input  d,
  output s
);

  wire and_1_out, and_2_out, and_3_out, not_1_out, not_2_out, or_1_out;

  not not_1 (not_1_out, a);
  not not_2 (not_2_out, c);
  or or_1 (or_1_out, c, d);
  and and_1 (and_1_out, not_1_out, c);
  and and_2 (and_2_out, b, or_1_out);
  and and_3 (and_3_out, a, not_2_out, d);
  or or_2 (s, and_1_out, and_2_out, and_3_out);

  // Notes on the sheet:
  //   Bruno César Lopes Silva - 415985
endmodule
