// Logisim project Exercicio 04.circ as structural Verilog: 1 circuit, main circuit main
module main (
  input  a,
  input  b,
  input  c,
  input  d,
  output out_5
);

  wire nand_1_out, nand_2_out, nand_3_out, nand_4_out, nand_5_out, nand_6_out, nand_7_out, nand_8_out,
       nand_9_out, nand_10_out, nand_11_out, nand_12_out;

  nand nand_1 (nand_1_out, a, a);
  nand nand_2 (nand_2_out, c, c);
  nand nand_3 (nand_3_out, nand_1_out, c);
  nand nand_4 (nand_4_out, b, d);
  nand nand_5 (nand_5_out, nand_3_out, nand_4_out);
  nand nand_6 (nand_6_out, a, nand_2_out);
  nand nand_7 (nand_7_out, b, c);
  nand nand_8 (nand_8_out, nand_5_out, nand_5_out);
  nand nand_9 (nand_9_out, nand_6_out, nand_6_out);
  nand nand_10 (nand_10_out, nand_9_out, d);
  nand nand_11 (nand_11_out, nand_7_out, nand_10_out);
  nand nand_12 (nand_12_out, nand_11_out, nand_11_out);
  nand nand_13 (out_5, nand_12_out, nand_8_out);

  // Notes on the sheet:
  //   Bruno César Lopes Silva - 415985
endmodule
