// Logisim project Exercicio 05.circ as structural Verilog: 1 circuit, main circuit main
module main (
  input  a,
  input  b,
  input  c,
  input  d,
  output s
);

  wire nor_1_out, nor_2_out, nor_3_out, nor_4_out, nor_5_out, nor_6_out, nor_7_out, nor_8_out;

  nor nor_1 (nor_1_out, a, a);
  nor nor_2 (nor_2_out, d, d);
  nor nor_3 (nor_3_out, nor_1_out, nor_2_out);
  nor nor_4 (nor_4_out, a, d);
  nor nor_5 (nor_5_out, b, c);
  nor nor_6 (nor_6_out, nor_5_out, nor_5_out);
  nor nor_7 (nor_7_out, nor_6_out, d);
  nor nor_8 (nor_8_out, nor_3_out, nor_4_out, nor_7_out);
  nor nor_9 (s, nor_8_out, nor_8_out);

  // Notes on the sheet:
  //   Bruno Cesar Lopes Silva - 415985
endmodule
