// Logisim project guia08-01.circ as structural Verilog: 1 circuit, main circuit main
module main (
  input  a,
  input  b,
  input  c,
  input  d,
  output s
);

  wire and_1_out, and_2_out, and_3_out, and_4_out, not_1_out, not_2_out;

  not not_1 (not_1_out, c);
  and and_1 (and_1_out, a, not_1_out, d);
  not not_2 (not_2_out, a);
  and and_2 (and_2_out, not_2_out, c);
  and and_3 (and_3_out, b, d);
  or or_1 (s, and_1_out, and_2_out, and_3_out, and_4_out);
  and and_4 (and_4_out, b, c);
endmodule
