// Logisim project guia08-03.circ as structural Verilog: 1 circuit, main circuit main
module main (
  input  a,
  input  a_2,
  input  b,
  input  b_2,
  input  c,
  input  c_2,
  input  d,
  input  d_2,
  input  e,
  input  e_2,
  output s,
  output s_2
);

  wire not_1_out, not_2_out, not_3_out, not_4_out, not_5_out, not_6_out, not_7_out, not_8_out, not_9_out,
       not_10_out, not_11_out, or_1_out, or_2_out, or_3_out, or_4_out, or_5_out, or_6_out;

  not not_1 (not_1_out, d);
  not not_2 (not_2_out, b);
  or or_1 (or_1_out, a, not_2_out, c, not_1_out);
  not not_3 (not_3_out, c);
  not not_4 (not_4_out, d);
  or or_2 (or_2_out, a, not_3_out, not_4_out, e);
  and and_1 (s, or_1_out, or_2_out, or_3_out);
  not not_5 (not_5_out, c);
  or or_3 (or_3_out, a, not_5_out, e);
  not not_6 (not_6_out, a_2);
  or or_4 (or_4_out, not_6_out, b_2, c_2, d_2, e_2);
  not not_7 (not_7_out, c_2);
  not not_8 (not_8_out, a_2);
  or or_5 (or_5_out, not_8_out, not_7_out, not_9_out, e_2);
  and and_2 (s_2, or_4_out, or_5_out, or_6_out);
  not not_9 (not_9_out, d_2);
  not not_10 (not_10_out, b_2);
  not not_11 (not_11_out, a_2);
  or or_6 (or_6_out, not_11_out, not_10_out, c_2);
endmodule
