// Logisim project guia08-04.circ as structural Verilog: 1 circuit, main circuit main
module main (
  input  a,
  input  b,
  input  c,
  input  d,
  output s
);

  wire nand_1_out, nand_2_out, nand_3_out, nand_4_out, nand_5_out, nand_6_out, nand_7_out, nand_8_out,
       nand_9_out, nand_11_out, nand_12_out, nand_13_out, not_1_out, not_2_out;

  not not_1 (not_1_out, c);
  nand nand_1 (nand_1_out, a, not_1_out, d);
  nand nand_2 (nand_2_out, nand_1_out, nand_1_out);
  nand nand_3 (nand_3_out, nand_2_out, nand_2_out);
  not not_2 (not_2_out, a);
  nand nand_4 (nand_4_out, not_2_out, c);
  nand nand_5 (nand_5_out, nand_4_out, nand_4_out);
  nand nand_6 (nand_6_out, nand_5_out, nand_5_out);
  nand nand_7 (nand_7_out, b, d);
  nand nand_8 (nand_8_out, nand_7_out, nand_7_out);
  nand nand_9 (nand_9_out, nand_8_out, nand_8_out);
  nand nand_10 (s, nand_3_out, nand_6_out, nand_9_out, nand_13_out);
  nand nand_11 (nand_11_out, b, c);
  nand nand_12 (nand_12_out, nand_11_out, nand_11_out);
  nand nand_13 (nand_13_out, nand_12_out, nand_12_out);
endmodule
