// Logisim project guia08-05.circ as structural Verilog: 1 circuit, main circuit main
module main (
  input  a,
  input  b,
  input  c,
  input  d,
  output s
);

  wire nor_1_out, nor_2_out, nor_3_out, nor_4_out, nor_5_out, nor_6_out, nor_7_out, nor_9_out, nor_10_out,
       nor_11_out, nor_12_out, not_1_out, not_2_out, not_3_out, not_4_out;

  nor nor_1 (nor_1_out, a, a);
  not not_1 (not_1_out, c);
  not not_2 (not_2_out, b);
  nor nor_2 (nor_2_out, not_2_out, not_2_out);
  nor nor_3 (nor_3_out, nor_1_out, nor_2_out, nor_4_out);
  nor nor_4 (nor_4_out, not_1_out, not_1_out);
  not not_3 (not_3_out, a);
  nor nor_5 (nor_5_out, not_3_out, not_3_out);
  nor nor_6 (nor_6_out, nor_5_out, nor_9_out);
  nor nor_7 (nor_7_out, nor_3_out, nor_6_out, nor_12_out);
  nor nor_8 (s, nor_7_out, nor_7_out);
  not not_4 (not_4_out, d);
  nor nor_9 (nor_9_out, not_4_out, not_4_out);
  nor nor_10 (nor_10_out, a, a);
  nor nor_11 (nor_11_out, d, d);
  nor nor_12 (nor_12_out, nor_10_out, nor_11_out);
endmodule
