// Logisim project Exercicio02.circ as structural Verilog: 1 circuit, main circuit main
module main (
  input  c,
  input  b,
  input  a,
  input  d,
  output out
);

  wire and_1_out, and_2_out, and_3_out, not_1_out, not_2_out, not_3_out, not_4_out;

  not not_1 (not_1_out, a);
  not not_2 (not_2_out, d);
  not not_3 (not_3_out, b);
  not not_4 (not_4_out, b);
  and and_1 (and_1_out, not_1_out, not_2_out);
  and and_2 (and_2_out, a, d);
  and and_3 (and_3_out, a, not_3_out, not_4_out);
  or or_1 (out, and_1_out, and_2_out, and_3_out);

  assign c = b;

  // Notes on the sheet:
  //   Alvaro Henrique - 395487
  //   Exercicio 02
endmodule
