// Logisim project Exercicio03.circ as structural Verilog: 1 circuit, main circuit main
module main (
  input  b,
  input  a,
  input  c,
  input  d,
  input  e,
  output out
);

  wire and_1_out, and_2_out, and_3_out, and_4_out, and_5_out, not_1_out, not_2_out, not_3_out, not_4_out;

  not not_1 (not_1_out, a);
  not not_2 (not_2_out, c);
  not not_3 (not_3_out, d);
  not not_4 (not_4_out, b);
  and and_1 (and_1_out, not_1_out, not_2_out, not_3_out);
  and and_2 (and_2_out, a, c, not_3_out);
  and and_3 (and_3_out, not_4_out, d);
  and and_4 (and_4_out, c, d);
  and and_5 (and_5_out, a, not_4_out, d, not_2_out);
  or or_1 (out, and_1_out, and_2_out, and_3_out, and_4_out, and_5_out);

  assign e = d;

  // Notes on the sheet:
  //   Alvaro Henrique - 395487
  //   Exercicio 03
endmodule
