// Logisim project Guia08.circ as structural Verilog: 3 circuits, main circuit Ex01
module Ex01 (
  input  a,
  input  b,
  input  c,
  input  d,
  output out
);

  wire and_1_out, and_2_out, and_3_out, and_4_out, not_1_out, not_2_out;

  not not_1 (not_1_out, a);
  not not_2 (not_2_out, a);
  and and_1 (and_1_out, not_1_out, a);
  and and_2 (and_2_out, a, a);
  and and_3 (and_3_out, a, d, d);
  and and_4 (and_4_out, not_2_out, a, d);
  or or_1 (out, and_1_out, and_2_out, and_3_out, and_4_out);

  assign b = a;
  assign c = a;

  // Notes on the sheet:
  //   Anderson Belchior de Carvalho - 396673
  //   Guia08_01
endmodule

module Ex02 (
  input  a,
  input  b,
  input  c,
  input  d,
  output out
);

  wire and_1_out, and_2_out, and_3_out, not_1_out, not_2_out, not_3_out, not_4_out;

  not not_1 (not_1_out, a);
  not not_2 (not_2_out, d);
  not not_3 (not_3_out, b);
  not not_4 (not_4_out, b);
  and and_1 (and_1_out, not_1_out, not_2_out);
  and and_2 (and_2_out, a, d);
  and and_3 (and_3_out, a, not_3_out, not_4_out);
  or or_1 (out, and_1_out, and_2_out, and_3_out);

  // Notes on the sheet:
  //   c1
  //   c2
  //   c3
  //   Anderson Belchior de Carvalho - 396673
  //   Guia08 - 02
endmodule

module Ex03 (
  input  a,
  input  b,
  input  c,
  input  d,
  input  e,
  output out
);

  wire and_1_out, and_2_out, and_3_out, and_4_out, and_5_out, not_1_out, not_2_out, not_3_out, not_4_out;

  not not_1 (not_1_out, a);
  not not_2 (not_2_out, c);
  not not_3 (not_3_out, d);
  not not_4 (not_4_out, b);
  and and_1 (and_1_out, not_1_out, not_2_out, not_3_out);
  and and_2 (and_2_out, a, c, not_3_out);
  and and_3 (and_3_out, not_4_out, e);
  and and_4 (and_4_out, c, e);
  and and_5 (and_5_out, a, not_4_out, d, not_2_out);
  or or_1 (out, and_1_out, and_2_out, and_3_out, and_4_out, and_5_out);

  // Notes on the sheet:
  //   c1
  //   c2
  //   c3
  //   c4
  //   c5
  //   Anderson Belchior de Carvalho - 396673
  //   Guia08 - 03
endmodule
