// Logisim project guia08_01.circ as structural Verilog: 1 circuit, main circuit Exercicio1
module Exercicio1 (
  input  a,
  input  b,
  input  c,
  input  d,
  output out
);

  wire and_1_out, and_2_out, and_3_out, and_4_out, not_1_out, not_2_out;

  not not_1 (not_1_out, a);
  not not_2 (not_2_out, c);
  and and_1 (and_1_out, not_1_out, c);
  and and_2 (and_2_out, b, c);
  and and_3 (and_3_out, b, d, d);
  and and_4 (and_4_out, not_2_out, a, d);
  or or_1 (out, and_1_out, and_2_out, and_3_out, and_4_out);

  // Notes on the sheet:
  //   Anderson Belchior de Carvalho - 396673
  //   Guia08_01
endmodule
