// Logisim project guia8.circ as structural Verilog
module EX1 (
  input  a,
  input  b,
  input  c,
  input  d,
  output out_5
);

  wire and_1_out, and_2_out, and_3_out, and_4_out, not_1_out, not_2_out;

  not not_1 (not_1_out, a);
  not not_2 (not_2_out, c);
  and and_1 (and_1_out, not_1_out, c);
  buf and_2 (and_2_out, b);  // AND_Gate
  and and_3 (and_3_out, b, d);
  and and_4 (and_4_out, not_2_out, d, a);
  or or_1 (out_5, and_1_out, and_2_out, and_3_out, and_4_out);
endmodule

module EX2 (
  input  a,
  input  b,
  input  c,
  input  d,
  output out_5
);

  wire and_1_out, and_2_out, and_3_out, not_1_out, not_2_out, not_3_out, not_4_out;

  not not_1 (not_1_out, a);
  not not_2 (not_2_out, d);
  not not_3 (not_3_out, b);
  not not_4 (not_4_out, b);
  and and_1 (and_1_out, not_1_out, not_2_out);
  and and_2 (and_2_out, a, d);
  and and_3 (and_3_out, a, not_3_out, not_4_out);
  or or_1 (out_5, and_1_out, and_2_out, and_3_out);
endmodule

module EX3 (
  input  a,
  input  b,
  input  c,
  input  d,
  input  e,
  output out_6
);

  wire and_1_out, and_2_out, and_3_out, and_4_out, and_5_out, not_1_out, not_2_out, not_3_out, not_4_out,
       not_5_out, not_6_out, not_7_out;

  not not_1 (not_1_out, a);
  not not_2 (not_2_out, c);
  not not_3 (not_3_out, d);
  not not_4 (not_4_out, d);
  not not_5 (not_5_out, b);
  not not_6 (not_6_out, c);
  not not_7 (not_7_out, b);
  and and_1 (and_1_out, not_1_out, not_2_out, not_3_out);
  and and_2 (and_2_out, a, c, not_4_out);
  and and_3 (and_3_out, not_5_out, e);
  and and_4 (and_4_out, c, e);
  and and_5 (and_5_out, a, not_6_out, not_7_out, d);
  or or_1 (out_6, and_1_out, and_2_out, and_3_out, and_4_out, and_5_out);
endmodule
