// Logisim project Guia0801.circ as structural Verilog: 1 circuit, main circuit main
module main (
  input  [3:0] a,
  output s
);

  wire and_1_out, and_2_out, and_3_out, not_1_out, not_2_out, not_3_out;

  not not_1 (not_1_out, a[0]);
  not not_2 (not_2_out, a[2]);
  not not_3 (not_3_out, a[3]);
  and and_1 (and_1_out, not_1_out, a[2], a[3]);
  and and_2 (and_2_out, a[1], not_2_out);
  and and_3 (and_3_out, a[1], not_3_out);
  or or_1 (s, and_1_out, and_2_out, and_3_out);

  // Notes on the sheet:
  //   Pedro Tronbin  - Guia 08 Exercicio01
  //   Simplificacao (Vide Verilog):
  //   (~a2.a1) + (~a3.a1) + (a3.a2.~a0)
endmodule
