// Logisim project Guia0804.circ as structural Verilog: 1 circuit, main circuit main
module main (
  input  [3:0] a,
  output s
);

  wire nand_1_out, nand_2_out, nand_3_out, nand_4_out, nand_5_out, nand_6_out, nand_7_out, nand_8_out,
       nand_9_out, nand_10_out, nand_11_out, nand_12_out;

  not nand_1 (nand_1_out, a[0]);  // NAND_Gate
  not nand_2 (nand_2_out, a[2]);  // NAND_Gate
  not nand_3 (nand_3_out, a[3]);  // NAND_Gate
  nand nand_4 (nand_4_out, nand_1_out, a[2], a[3]);
  nand nand_5 (nand_5_out, a[1], nand_2_out);
  not nand_6 (nand_6_out, nand_5_out);  // NAND_Gate
  nand nand_7 (nand_7_out, a[1], nand_3_out);
  not nand_8 (nand_8_out, nand_7_out);  // NAND_Gate
  not nand_9 (nand_9_out, nand_4_out);  // NAND_Gate
  not nand_10 (nand_10_out, nand_9_out);  // NAND_Gate
  not nand_11 (nand_11_out, nand_6_out);  // NAND_Gate
  not nand_12 (nand_12_out, nand_8_out);  // NAND_Gate
  nand nand_13 (s, nand_10_out, nand_11_out, nand_12_out);

  // Notes on the sheet:
  //   Pedro Tronbin  - Guia 08 Exercicio04
  //   Simplificacao (Vide Verilog):
  //   (~a2.a1) + (~a3.a1) + (a3.a2.~a0)
endmodule
