// Logisim project guia8.circ as structural Verilog: 3 circuits, main circuit exercici01
module exercici01 (
  input  a,
  input  b,
  input  c,
  input  d,
  output saida
);

  wire and_1_out, and_2_out, and_3_out, and_4_out, not_1_out, not_2_out, not_3_out, not_4_out, not_5_out,
       not_6_out;

  not not_1 (not_1_out, c);
  not not_2 (not_2_out, a);
  not not_3 (not_3_out, a);
  not not_4 (not_4_out, b);
  not not_5 (not_5_out, d);
  not not_6 (not_6_out, d);
  and and_1 (and_1_out, not_4_out, not_1_out, not_5_out);
  and and_2 (and_2_out, a, c, c);
  and and_3 (and_3_out, a, b, d);
  and and_4 (and_4_out, not_2_out, not_6_out);
  // AND_Gate and_5 has open pins: in0=not_6_out, in3=not_3_out, out=open
  or or_1 (saida, and_1_out, and_2_out, and_3_out, and_4_out);
endmodule

module exercicio02 (
  input  a,
  input  b,
  input  c,
  input  d,
  output out_5
);

  wire and_1_out, and_2_out, and_3_out, and_4_out, not_1_out, not_2_out;

  not not_1 (not_1_out, a);
  not not_2 (not_2_out, c);
  and and_1 (and_1_out, not_1_out, not_2_out, d);
  and and_2 (and_2_out, not_1_out, c);
  and and_3 (and_3_out, b, d);
  and and_4 (and_4_out, b, c);
  or or_1 (out_5, and_1_out, and_2_out, and_3_out, and_4_out);
endmodule

module exercicio3 (
  input  a,
  input  b,
  input  c,
  input  d,
  input  e,
  output saida
);

  wire and_1_out, and_2_out, and_3_out, and_4_out, and_5_out, and_6_out, and_7_out, not_1_out, not_2_out,
       not_3_out, not_4_out, not_5_out, not_6_out, not_7_out, not_8_out, not_9_out, not_10_out;

  not not_1 (not_1_out, b);
  not not_2 (not_2_out, d);
  not not_3 (not_3_out, a);
  not not_4 (not_4_out, c);
  not not_5 (not_5_out, d);
  not not_6 (not_6_out, a);
  not not_7 (not_7_out, b);
  not not_8 (not_8_out, a);
  not not_9 (not_9_out, b);
  not not_10 (not_10_out, c);
  and and_1 (and_1_out, not_3_out, not_4_out, not_5_out);
  and and_2 (and_2_out, not_6_out, not_7_out, e);
  and and_3 (and_3_out, not_8_out, c, e);
  and and_4 (and_4_out, a, not_9_out, not_10_out, e);
  and and_5 (and_5_out, not_1_out, a, c);
  and and_6 (and_6_out, a, c, not_2_out);
  and and_7 (and_7_out, e, a, c);
  or or_1 (saida, and_4_out, and_1_out, and_2_out, and_3_out, and_5_out, and_6_out, and_7_out);
endmodule
