// Logisim project Lab008.circ as structural Verilog
module funcaoSoP1 (
  input  a,
  input  b,
  input  c,
  input  d,
  output s
);

  wire AND1_out, AND2_out, AND3_out, AND4_out, not_1_out, not_2_out;

  not not_1 (not_1_out, a);
  not not_2 (not_2_out, c);
  and AND4 (AND4_out, c, b);
  and AND2 (AND2_out, not_1_out, c);
  and AND1 (AND1_out, d, not_2_out, a);
  and AND3 (AND3_out, d, b);
  or OR1 (s, AND4_out, AND2_out, AND1_out, AND3_out);

  // Notes on the sheet:
  //   Karen Alves - Exercicio 01
endmodule

module funcaoSop2 (
  input  a,
  input  b,
  input  c,
  input  d,
  output s
);

  wire AND1_out, AND2_out, AND3_out, not_1_out, not_2_out, not_3_out, not_4_out;

  not not_1 (not_1_out, c);
  not not_2 (not_2_out, b);
  not not_3 (not_3_out, d);
  not not_4 (not_4_out, a);
  and AND3 (AND3_out, d, a);
  and AND2 (AND2_out, not_3_out, not_4_out);
  and AND1 (AND1_out, not_1_out, not_2_out, a);
  or OR1 (s, AND3_out, AND2_out, AND1_out);

  // Notes on the sheet:
  //   Karen Alves - Exercicio 02
endmodule

module simplificacaoQM (
  input  a,
  input  b,
  input  c,
  input  d,
  input  e,
  output s
);

  wire AND1_out, AND2_out, AND3_out, AND4_out, AND5_out, not_1_out, not_2_out, not_3_out, not_4_out,
       not_5_out, not_6_out;

  not not_1 (not_1_out, a);
  not not_2 (not_2_out, b);
  not not_3 (not_3_out, c);
  not not_4 (not_4_out, d);
  and AND5 (AND5_out, d, not_3_out, a);
  not not_5 (not_5_out, b);
  not not_6 (not_6_out, d);
  and AND1 (AND1_out, not_4_out, not_3_out, not_1_out);
  and AND2 (AND2_out, not_6_out, c, a);
  and AND3 (AND3_out, e, not_5_out);
  and AND4 (AND4_out, e, c);
  or OR1 (s, AND4_out, AND3_out, AND2_out, AND1_out, AND5_out);

  // Notes on the sheet:
  //   Jessica Luisa Betonico Andrade -  412748
endmodule
