// Logisim project Guia08.circ as structural Verilog: 5 circuits, main circuit Ex_01
module Ex_01 (
  input  A,
  input  B,
  input  C,
  input  D,
  output S
);

  wire A_prime_C_out, AC_prime_D_out, BC_out, BD_out, not_1_out, not_2_out;

  not not_1 (not_1_out, A);
  not not_2 (not_2_out, C);
  and AC_prime_D (AC_prime_D_out, A, not_2_out, D);
  and A_prime_C (A_prime_C_out, not_1_out, C);
  and BD (BD_out, B, D);
  and BC (BC_out, B, C);
  or or_1 (S, AC_prime_D_out, A_prime_C_out, BD_out, BC_out);

  // Notes on the sheet:
  //   Aluno: Alyson Deives
  //   Guia 08_01 - Circuito SoP ( m( 2, 3, 5, 6, 7, 9, 13, 14, 15 ) ) 
  //   Matricula: 416589
endmodule

module Ex_02 (
  input  A,
  input  B,
  input  C,
  input  D,
  output S
);

  wire A_D_out, AB_prime_C_prime_out, ABD_out, not_1_out, not_2_out;

  not not_1 (not_1_out, C);
  not not_2 (not_2_out, B);
  and AB_prime_C_prime (AB_prime_C_prime_out, A, not_2_out, not_1_out);
  xnor A_D (A_D_out, A, D);
  and ABD (ABD_out, A, B, D);
  or or_1 (S, AB_prime_C_prime_out, A_D_out, ABD_out);

  // Notes on the sheet:
  //   Aluno: Alyson Deives
  //   Guia 08_02 - Circuito SoP ( m( 0, 2, 4, 6, 8, 9, 11, 13, 15 ) )
  //   Matricula: 416589
endmodule

module Ex_03 (
  input  A,
  input  B,
  input  C,
  input  D,
  input  E,
  output S
);

  wire A_C_out, AB_prime_C_prime_D_out, and_1_out, B_prime_E_out, CE_out, not_1_out, not_2_out, not_3_out;

  not not_1 (not_1_out, B);
  not not_2 (not_2_out, C);
  not not_3 (not_3_out, D);
  xnor A_C (A_C_out, A, C);
  and B_prime_E (B_prime_E_out, not_1_out, E);
  and CE (CE_out, C, E);
  and AB_prime_C_prime_D (AB_prime_C_prime_D_out, A, not_1_out, not_2_out, D);
  and and_1 (and_1_out, A_C_out, not_3_out);
  or or_1 (S, and_1_out, B_prime_E_out, CE_out, AB_prime_C_prime_D_out);

  // Notes on the sheet:
  //   Aluno: Alyson Deives
  //   Matricula: 416589
  //   Guia 08_03 - Circuito SoP ( m( 0,1,3,5,7,8,9,13,15,17,18,19,20,21,23,28,29,31) )
endmodule

module Ex_04 (
  input  A,
  input  B,
  input  C,
  input  D,
  output S
);

  wire nand_1_out, nand_2_out, nand_3_out, nand_4_out, nand_5_out, nand_6_out, nand_7_out, nand_8_out,
       nand_9_out, nand_10_out;

  nand nand_1 (nand_1_out, A, A);
  nand nand_2 (nand_2_out, C, C);
  nand nand_3 (nand_3_out, A, nand_2_out, D);
  nand nand_4 (nand_4_out, nand_1_out, C);
  nand nand_5 (nand_5_out, B, D);
  nand nand_6 (nand_6_out, B, C);
  nand nand_7 (nand_7_out, nand_3_out, nand_4_out);
  nand nand_8 (nand_8_out, nand_5_out, nand_6_out);
  nand nand_9 (nand_9_out, nand_7_out, nand_7_out);
  nand nand_10 (nand_10_out, nand_8_out, nand_8_out);
  nand nand_11 (S, nand_9_out, nand_10_out);

  // Notes on the sheet:
  //   Guia 08_04 - Circuito SoP ( m( 2, 3, 5, 6, 7, 9, 13, 14, 15 ) ) com portas NAND
  //   Aluno: Alyson Deives
  //   Matricula: 416589
endmodule

module Ex_05 (
  input  A,
  input  B,
  input  C,
  input  D,
  output S
);

  wire nor_1_out, nor_2_out, nor_3_out, nor_4_out, nor_5_out, nor_6_out, nor_7_out, nor_8_out, nor_9_out,
       nor_10_out, nor_11_out, nor_12_out, nor_13_out, nor_14_out, nor_15_out;

  nor nor_1 (nor_1_out, A, A);
  nor nor_2 (nor_2_out, A, D);
  nor nor_3 (nor_3_out, A, A);
  nor nor_4 (nor_4_out, B, B);
  nor nor_5 (nor_5_out, nor_1_out, B);
  nor nor_6 (nor_6_out, A, nor_2_out);
  nor nor_7 (nor_7_out, nor_2_out, D);
  nor nor_8 (nor_8_out, nor_3_out, nor_4_out);
  nor nor_9 (nor_9_out, nor_5_out, nor_5_out);
  nor nor_10 (nor_10_out, nor_6_out, nor_7_out);
  nor nor_11 (nor_11_out, nor_8_out, nor_8_out);
  nor nor_12 (nor_12_out, D, D);
  nor nor_13 (nor_13_out, nor_9_out, C);
  nor nor_14 (nor_14_out, nor_11_out, nor_12_out);
  nor nor_15 (nor_15_out, nor_13_out, nor_10_out, nor_14_out);
  nor nor_16 (S, nor_15_out, nor_15_out);

  // Notes on the sheet:
  //   Aluno: Alyson Deives
  //   Matricula: 416589
  //   Guia 08_05 - Circuito SoP ( m( 0, 2, 4, 6, 8, 9, 11, 13, 15 ) ) com portas NOR
endmodule
