// Logisim project guia08_04.circ as structural Verilog: 1 circuit, main circuit main
module main (
  input  a,
  input  b,
  input  c,
  input  d,
  output out_5
);

  wire nand_1_out, nand_2_out, nand_3_out, nand_4_out, nand_5_out, nand_6_out, nand_7_out, nand_8_out,
       nand_9_out, nand_10_out, nand_11_out, nand_12_out, nand_13_out, nand_14_out, nand_15_out, nand_16_out,
       not_1_out;

  not not_1 (not_1_out, a);
  nand nand_1 (nand_1_out, a, b, d);
  nand nand_2 (nand_2_out, not_1_out, c);
  nand nand_3 (nand_3_out, b, c);
  nand nand_4 (nand_4_out, d, d);
  not nand_5 (nand_5_out, nand_1_out);  // NAND_Gate
  not nand_6 (nand_6_out, nand_2_out);  // NAND_Gate
  not nand_7 (nand_7_out, nand_3_out);  // NAND_Gate
  not nand_8 (nand_8_out, nand_4_out);  // NAND_Gate
  nand nand_9 (nand_9_out, nand_5_out, nand_5_out);
  nand nand_10 (nand_10_out, nand_6_out, nand_6_out);
  nand nand_11 (nand_11_out, nand_7_out, nand_7_out);
  nand nand_12 (nand_12_out, nand_8_out, nand_8_out);
  nand nand_13 (nand_13_out, nand_9_out, nand_10_out);
  nand nand_14 (nand_14_out, nand_11_out, nand_12_out);
  nand nand_15 (nand_15_out, nand_13_out, nand_13_out);
  nand nand_16 (nand_16_out, nand_14_out, nand_14_out);
  nand nand_17 (out_5, nand_15_out, nand_16_out);

  // Notes on the sheet:
  //   LUIZ MARQUES DE OLIVEIRA - 417138
endmodule
