// Logisim project Guia08.circ as structural Verilog: 5 circuits, main circuit Ex01
module Ex01 (
  input  a,
  input  b,
  input  c,
  input  d,
  output s
);

  wire and_1_out, and_2_out, and_3_out, and_4_out, not_1_out, not_2_out;

  not not_1 (not_1_out, a);
  not not_2 (not_2_out, c);
  and and_1 (and_1_out, not_1_out, c);
  and and_2 (and_2_out, b, c);
  or or_1 (s, and_1_out, and_2_out, and_3_out, and_4_out);
  and and_3 (and_3_out, b, d);
  and and_4 (and_4_out, a, not_2_out, d);
endmodule

module Ex02 (
  input  a,
  input  b,
  input  c,
  input  d,
  output s
);

  wire and_1_out, and_2_out, and_3_out, not_1_out, not_2_out, not_3_out, not_4_out;

  not not_1 (not_1_out, a);
  not not_2 (not_2_out, d);
  not not_3 (not_3_out, b);
  not not_4 (not_4_out, c);
  and and_1 (and_1_out, not_1_out, not_2_out);
  or or_1 (s, and_1_out, and_2_out, and_3_out);
  and and_2 (and_2_out, a, d);
  and and_3 (and_3_out, a, not_3_out, not_4_out);
endmodule

module Ex03 (
  input  a,
  input  b,
  input  c,
  input  d,
  input  e,
  output out_6
);

  wire and_1_out, and_2_out, and_3_out, and_4_out, and_5_out, not_1_out, not_2_out, not_3_out, not_4_out,
       not_5_out, not_6_out, not_7_out;

  not not_1 (not_1_out, b);
  not not_2 (not_2_out, a);
  not not_3 (not_3_out, c);
  not not_4 (not_4_out, d);
  not not_5 (not_5_out, d);
  not not_6 (not_6_out, b);
  not not_7 (not_7_out, c);
  and and_1 (and_1_out, not_1_out, e);
  and and_2 (and_2_out, c, e);
  and and_3 (and_3_out, not_2_out, not_3_out, not_4_out);
  and and_4 (and_4_out, a, c, not_5_out);
  and and_5 (and_5_out, a, not_6_out, not_7_out, d);
  or or_1 (out_6, and_1_out, and_2_out, and_3_out, and_4_out, and_5_out);
endmodule

module Ex04 (
  input  a,
  input  b,
  input  c,
  input  d,
  output s
);

  wire nand_1_out, nand_2_out, nand_3_out, nand_4_out, nand_5_out, nand_6_out;

  nand nand_1 (nand_1_out, a, a);
  nand nand_2 (nand_2_out, c, c);
  nand nand_3 (nand_3_out, nand_1_out, c);
  nand nand_4 (nand_4_out, a, d);
  nand nand_5 (nand_5_out, b, d);
  nand nand_6 (nand_6_out, a, nand_2_out, d);
  nand nand_7 (s, nand_3_out, nand_4_out, nand_5_out, nand_6_out);
endmodule

module Ex05 (
  input  a,
  input  b,
  input  c,
  input  d,
  output s
);

  wire nor_1_out, nor_2_out, nor_3_out, nor_4_out, nor_5_out, nor_6_out, nor_7_out;

  nor nor_1 (nor_1_out, b, b);
  nor nor_2 (nor_2_out, c, c);
  nor nor_3 (nor_3_out, a, a);
  nor nor_4 (nor_4_out, a, d);
  nor nor_5 (nor_5_out, nor_1_out, nor_2_out);
  nor nor_6 (nor_6_out, nor_3_out, b, c);
  nor nor_7 (nor_7_out, nor_4_out, nor_5_out, nor_6_out);
  nor nor_8 (s, nor_7_out, nor_7_out);
endmodule
