// Logisim project guia08.circ as structural Verilog: 5 circuits, main circuit Exercicio01
module Exercicio01 (
  input  a,
  input  b,
  input  c,
  input  d,
  output saida
);

  wire and_1_out, and_2_out, and_3_out, and_4_out, not_1_out, not_2_out;

  not not_1 (not_1_out, c);
  not not_2 (not_2_out, a);
  and and_1 (and_1_out, a, not_1_out, d);
  and and_2 (and_2_out, not_2_out, c);
  and and_3 (and_3_out, b, d);
  and and_4 (and_4_out, b, c);
  or or_1 (saida, and_1_out, and_2_out, and_3_out, and_4_out);

  // Notes on the sheet:
  //   Isabella Gonçales - 420120
endmodule

module Exercicio02 (
  input  a,
  input  b,
  input  c,
  input  d,
  output saida
);

  wire and_1_out, and_2_out, and_3_out, and_4_out, not_1_out, not_2_out, not_3_out, not_4_out;

  not not_1 (not_1_out, b);
  not not_2 (not_2_out, d);
  not not_3 (not_3_out, b);
  not not_4 (not_4_out, c);
  and and_1 (and_1_out, not_1_out, not_2_out);
  and and_2 (and_2_out, a, d);
  and and_3 (and_3_out, a, b, d);
  and and_4 (and_4_out, a, not_3_out, not_4_out);
  or or_1 (saida, and_1_out, and_2_out, and_3_out, and_4_out);

  // Notes on the sheet:
  //   Isabella Gonçales - 420120
endmodule

module Exercicio03 (
  input  a,
  input  b,
  input  c,
  input  d,
  input  e,
  output saida
);

  wire and_1_out, and_2_out, and_3_out, and_4_out, and_5_out, not_1_out, not_2_out, not_3_out, not_4_out,
       not_5_out, not_6_out, not_7_out;

  not not_1 (not_1_out, a);
  not not_2 (not_2_out, c);
  and and_1 (and_1_out, not_1_out, not_2_out, not_3_out);
  not not_3 (not_3_out, d);
  and and_2 (and_2_out, a, c, not_4_out);
  not not_4 (not_4_out, d);
  not not_5 (not_5_out, b);
  and and_3 (and_3_out, not_5_out, e);
  and and_4 (and_4_out, c, e);
  not not_6 (not_6_out, b);
  and and_5 (and_5_out, a, not_6_out, not_7_out, d);
  not not_7 (not_7_out, c);
  or or_1 (saida, and_1_out, and_2_out, and_3_out, and_4_out, and_5_out);

  // Notes on the sheet:
  //   Isabella Gonçales - 420120
endmodule

module Exercicio04 (
  input  a,
  input  b,
  input  c,
  input  d,
  output saida
);

  wire and_1_out, nand_1_out, nand_2_out, nand_3_out, nand_4_out, nand_5_out, nand_6_out, nand_7_out,
       nand_8_out, nand_9_out;

  nand nand_1 (nand_1_out, c, c);
  nand nand_2 (nand_2_out, a, a);
  nand nand_3 (nand_3_out, b, d);
  nand nand_4 (nand_4_out, b, c);
  nand nand_5 (nand_5_out, a, nand_1_out, d);
  nand nand_6 (nand_6_out, nand_2_out, c);
  nand nand_7 (nand_7_out, nand_3_out, nand_3_out);
  nand nand_8 (nand_8_out, nand_4_out, nand_4_out);
  nand nand_9 (nand_9_out, nand_5_out, nand_5_out);
  and and_1 (and_1_out, nand_6_out, nand_6_out);
  nand nand_10 (saida, nand_9_out, and_1_out, nand_7_out, nand_8_out);

  // Notes on the sheet:
  //   t1
  //   t3
  //   t6
  //   t8
  //   Isabella Gonçales - 420120
  //   t4
  //   t7
  //   t9
  //   t2
  //   t5
  //   t10
endmodule

module Exercicio05 (
  input  a,
  input  b,
  input  c,
  input  d,
  output saida
);

  wire nor_1_out, nor_2_out, nor_3_out, nor_4_out, nor_5_out, nor_6_out, nor_7_out, nor_8_out, nor_9_out,
       nor_10_out, nor_11_out, nor_12_out, nor_13_out, nor_14_out, nor_15_out, nor_16_out, nor_17_out;

  nor nor_1 (nor_1_out, b, b);
  nor nor_2 (nor_2_out, d, d);
  nor nor_3 (nor_3_out, a, a);
  nor nor_4 (nor_4_out, d, d);
  nor nor_5 (nor_5_out, a, a);
  nor nor_6 (nor_6_out, d, d);
  nor nor_7 (nor_7_out, c, c);
  nor nor_8 (nor_8_out, nor_1_out, nor_1_out);
  nor nor_9 (nor_9_out, nor_2_out, nor_2_out);
  nor nor_10 (nor_10_out, nor_3_out, nor_4_out);
  nor nor_11 (nor_11_out, nor_5_out, b, nor_6_out);
  nor nor_12 (nor_12_out, b, b);
  nor nor_13 (nor_13_out, nor_8_out, nor_9_out);
  nor nor_14 (nor_14_out, a, a);
  nor nor_15 (nor_15_out, nor_7_out, nor_7_out);
  nor nor_16 (nor_16_out, nor_14_out, nor_12_out, nor_15_out);
  nor nor_17 (nor_17_out, nor_13_out, nor_10_out, nor_11_out, nor_16_out);
  nor nor_18 (saida, nor_17_out, nor_17_out);

  // Notes on the sheet:
  //   t1
  //   t2
  //   t6
  //   t7
  //   t9
  //   t10
  //   Isabella Gonçales - 420120
  //   t8
  //   t13
  //   t14
  //   t3
  //   t5
  //   t4
  //   t11
  //   t12
  //   t15
  //   t16
  //   t17
endmodule
