// Logisim project Guia08.circ as structural Verilog: 3 circuits, main circuit SOP1
module SOP1 (
  input  a,
  input  b,
  input  c,
  input  d,
  output s
);

  wire and_1_out, and_2_out, and_3_out, and_4_out, not_1_out, not_2_out;

  not not_1 (not_1_out, a);
  not not_2 (not_2_out, c);
  and and_1 (and_1_out, not_1_out, c);
  and and_2 (and_2_out, b, c);
  and and_3 (and_3_out, b, d, d);
  and and_4 (and_4_out, not_2_out, a, d);
  or or_1 (s, and_1_out, and_2_out, and_3_out, and_4_out);

  // Notes on the sheet:
  //   t1
  //   t2
  //   t3
  //   t4
endmodule

module SOP2 (
  input  a,
  input  b,
  input  c,
  input  d,
  output s
);

  wire and_1_out, and_2_out, and_3_out, not_1_out, not_2_out, not_3_out, not_4_out;

  not not_1 (not_1_out, a);
  not not_2 (not_2_out, d);
  not not_3 (not_3_out, b);
  not not_4 (not_4_out, b);
  and and_1 (and_1_out, not_1_out, not_2_out);
  and and_2 (and_2_out, a, d);
  and and_3 (and_3_out, a, not_3_out, not_4_out);
  or or_1 (s, and_1_out, and_3_out, and_2_out);

  // Notes on the sheet:
  //   t2
  //   t3
  //   t1
endmodule

module Karnaugh (
  input  a,
  input  b,
  input  c,
  input  d,
  input  e,
  output s
);

  wire and_1_out, and_2_out, and_3_out, and_4_out, and_5_out, not_1_out, not_2_out, not_3_out, not_4_out;

  not not_1 (not_1_out, a);
  not not_2 (not_2_out, c);
  not not_3 (not_3_out, d);
  not not_4 (not_4_out, b);
  and and_1 (and_1_out, not_1_out, not_2_out, not_3_out);
  and and_2 (and_2_out, a, c, not_3_out);
  and and_3 (and_3_out, not_4_out, e);
  and and_4 (and_4_out, c, e);
  and and_5 (and_5_out, a, not_4_out, d, not_2_out);
  or or_1 (s, and_1_out, and_2_out, and_3_out, and_4_out, and_5_out);

  // Notes on the sheet:
  //   t1
  //   t2
  //   t3
  //   t4
  //   t5
endmodule
