// Logisim project Guia09.circ as structural Verilog: 1 circuit, main circuit Execicio02
module Execicio02 (
  input  in_1,
  output out_2
);

  wire clock_1_out, j_k_ff_1_q;

  Clock clock_1 (.out(clock_1_out));
  J_K_Flip_Flop j_k_ff_1 (.J(in_1), .clk(clock_1_out), .K(in_1), .Q(j_k_ff_1_q));  // open: Qn, preset, en, reset
  J_K_Flip_Flop j_k_ff_2 (.J(in_1), .clk(j_k_ff_1_q), .K(in_1), .Q(out_2));  // open: Qn, preset, en, reset

  // Notes on the sheet:
  //   Isabella Gonçales - 420120
endmodule
