// Logisim project Exercicio02.circ as structural Verilog: 1 circuit, main circuit main
module main (
  input  A,
  output S,
  output S_prime_prime
);

  wire CLK_out, JK_01_q;

  J_K_Flip_Flop JK_01 (.J(A), .clk(CLK_out), .K(A), .Q(JK_01_q));  // open: Qn, preset, en, reset
  Clock CLK (.out(CLK_out));
  J_K_Flip_Flop JK_02 (.J(A), .clk(JK_01_q), .K(A), .Q(S), .Qn(S_prime_prime));  // open: preset, en, reset
endmodule
