// Logisim project Guia10.circ as structural Verilog: 5 circuits, main circuit exercicio01
module exercicio01 (
  input  S,
  input  R,
  output Q,
  output Q_prime
);

  nor nor_1 (Q, S, Q_prime);
  nor nor_2 (Q_prime, Q, R);

  // Notes on the sheet:
  //   Caio Ragacci Pimentel - 405794
  //   Guia 10 - 01
endmodule

module exercicio02 (
  input  PR_prime,
  input  S,
  input  C,
  input  R,
  input  CR_prime,
  output Q,
  output Q_prime
);

  wire nand_1_out, nand_2_out;

  nand nand_1 (nand_1_out, S, C);
  nand nand_2 (nand_2_out, C, R);
  nand nand_3 (Q, PR_prime, nand_1_out, Q_prime);
  nand nand_4 (Q_prime, Q, nand_2_out, CR_prime);

  // Notes on the sheet:
  //   Caio Ragacci Pimentel - 405794
  //   Guia 10 - 02
endmodule

module exercicio03 (
  input  D,
  input  C,
  output Q,
  output Q_prime
);

  wire nand_1_out, nand_2_out, not_1_out;

  not not_1 (not_1_out, C);
  nand nand_1 (nand_1_out, D, C);
  not nand_2 (nand_2_out, not_1_out);  // NAND_Gate
  nand nand_3 (Q, nand_1_out, Q_prime);
  nand nand_4 (Q_prime, Q, nand_2_out);

  // Notes on the sheet:
  //   Caio Ragacci Pimentel - 405794
  //   Guia 10 - 03
endmodule

module exercicio04 (
  input  PR,
  input  S,
  input  R,
  input  CL,
  output Q,
  output Q_prime
);

  nand nand_1 (Q, PR, S, Q_prime);
  nand nand_2 (Q_prime, Q, R, CL);

  // Notes on the sheet:
  //   Caio Ragacci Pimentel - 405794
  //   Guia 10 - 04
endmodule

module exercicio05 (
  input  in_1,
  output Q,
  output QNot
);

  wire not_1_out;

  exercicio01 exercicio01_1 (.S(in_1), .R(not_1_out), .Q(Q), .Q_prime(QNot));
  not not_1 (not_1_out, in_1);

  // Notes on the sheet:
  //   Caio Ragacci Pimentel - 405794
  //   Guia 10 - 05
endmodule
