// Logisim project Circuitos.circ as structural Verilog
module Exercicio04 (
  input  DATA,
  input  RST,
  output s
);

  wire and_1_out, and_2_out, and_3_out, and_4_out, and_5_out, and_6_out, CLK_out, d_ff_1_q, d_ff_1_qn,
       d_ff_2_q, d_ff_2_qn, d_ff_3_q, d_ff_4_q, d_ff_4_qn, d_ff_5_q, d_ff_5_qn, or_1_out, or_2_out, or_3_out;

  Clock CLK (.out(CLK_out));
  and and_1 (and_1_out, d_ff_1_qn, d_ff_2_qn, d_ff_1_qn);
  D_Flip_Flop d_ff_1 (.clk(CLK_out), .D(DATA), .Q(d_ff_1_q), .Qn(d_ff_1_qn), .reset(RST));  // open: preset, en
  and and_2 (and_2_out, d_ff_1_q, d_ff_2_q, d_ff_3_q);
  or or_1 (or_1_out, and_1_out, and_2_out);
  D_Flip_Flop d_ff_2 (.clk(CLK_out), .D(d_ff_1_q), .Q(d_ff_2_q), .Qn(d_ff_2_qn), .reset(RST));  // open: preset, en
  and and_3 (and_3_out, d_ff_2_qn, d_ff_1_qn, d_ff_4_qn);
  D_Flip_Flop d_ff_3 (.clk(CLK_out), .D(d_ff_2_q), .Q(d_ff_3_q), .Qn(d_ff_1_qn), .reset(RST));  // open: preset, en
  and and_4 (and_4_out, d_ff_2_q, d_ff_3_q, d_ff_4_q);
  or or_2 (or_2_out, and_3_out, and_4_out);
  D_Flip_Flop d_ff_4 (.clk(CLK_out), .D(d_ff_3_q), .Q(d_ff_4_q), .Qn(d_ff_4_qn), .reset(RST));  // open: preset, en
  and and_5 (and_5_out, d_ff_1_qn, d_ff_4_qn, d_ff_5_qn);
  D_Flip_Flop d_ff_5 (.clk(CLK_out), .D(d_ff_4_q), .Q(d_ff_5_q), .Qn(d_ff_5_qn), .reset(RST));  // open: preset, en
  and and_6 (and_6_out, d_ff_3_q, d_ff_4_q, d_ff_5_q);
  or or_3 (or_3_out, and_5_out, and_6_out);
  or or_4 (s, or_3_out, or_2_out, or_1_out);

  // Notes on the sheet:
  //   Isabella Gonçales - 420120
endmodule

module Exercicio05 (
  input  DATA,
  input  RST,
  output s
);

  wire and_1_out, and_2_out, and_3_out, and_4_out, and_5_out, and_6_out, CLK_out, d_ff_1_q, d_ff_1_qn,
       d_ff_2_q, d_ff_2_qn, d_ff_3_q, d_ff_3_qn, d_ff_4_q, d_ff_4_qn, d_ff_5_q, d_ff_5_qn, or_1_out,
       or_2_out, or_3_out;

  Clock CLK (.out(CLK_out));
  D_Flip_Flop d_ff_1 (.clk(CLK_out), .D(DATA), .Q(d_ff_1_q), .Qn(d_ff_1_qn), .reset(RST));  // open: preset, en
  and and_1 (and_1_out, d_ff_1_qn, d_ff_2_q, d_ff_3_qn);
  D_Flip_Flop d_ff_2 (.clk(CLK_out), .D(d_ff_1_q), .Q(d_ff_2_q), .Qn(d_ff_2_qn), .reset(RST));  // open: preset, en
  and and_2 (and_2_out, d_ff_1_q, d_ff_2_qn, d_ff_3_q);
  or or_1 (or_1_out, and_1_out, and_2_out);
  D_Flip_Flop d_ff_3 (.clk(CLK_out), .D(d_ff_2_q), .Q(d_ff_3_q), .Qn(d_ff_3_qn), .reset(RST));  // open: preset, en
  and and_3 (and_3_out, d_ff_2_qn, d_ff_3_q, d_ff_4_qn);
  and and_4 (and_4_out, d_ff_2_q, d_ff_3_qn, d_ff_4_q);
  or or_2 (or_2_out, and_3_out, and_4_out);
  D_Flip_Flop d_ff_4 (.clk(CLK_out), .D(d_ff_3_q), .Q(d_ff_4_q), .Qn(d_ff_4_qn), .reset(RST));  // open: preset, en
  and and_5 (and_5_out, d_ff_3_qn, d_ff_4_q, d_ff_5_qn);
  D_Flip_Flop d_ff_5 (.clk(CLK_out), .D(d_ff_4_q), .Q(d_ff_5_q), .Qn(d_ff_5_qn), .reset(RST));  // open: preset, en
  and and_6 (and_6_out, d_ff_3_q, d_ff_4_qn, d_ff_5_q);
  or or_3 (or_3_out, and_5_out, and_6_out);
  or or_4 (s, or_3_out, or_2_out, or_1_out);

  // Notes on the sheet:
  //   Isabella Gonçales - 420120
endmodule
