// Logisim project exercicio02.circ as structural Verilog: 1 circuit, main circuit main
module main (
  input  in_1,
  output out_2
);

  wire and_1_out, clock_1_out, d_ff_1_q, d_ff_2_q, d_ff_3_q, d_ff_4_q, nor_1_out, not_1_out, t_ff_1_q,
       t_ff_2_q;

  Clock clock_1 (.out(clock_1_out));
  T_Flip_Flop t_ff_1 (
    .clk(clock_1_out), .T(t_ff_2_q), .Q(t_ff_1_q), .preset(1'b0), .reset(1'b0), .en(1'b1));  // open: Qn
  D_Flip_Flop d_ff_1 (.clk(clock_1_out), .D(in_1), .Q(d_ff_1_q), .preset(1'b0), .en(1'b1), .reset(1'b0));  // open: Qn
  T_Flip_Flop t_ff_2 (.clk(clock_1_out), .T(1'b1), .Q(t_ff_2_q), .preset(1'b0), .reset(1'b0), .en(1'b1));  // open: Qn
  D_Flip_Flop d_ff_2 (
    .clk(clock_1_out), .D(d_ff_1_q), .Q(d_ff_2_q), .preset(nor_1_out), .en(1'b1), .reset(1'b0));  // open: Qn
  D_Flip_Flop d_ff_3 (
    .clk(clock_1_out), .D(d_ff_2_q), .Q(d_ff_3_q), .preset(nor_1_out), .en(1'b1), .reset(1'b0));  // open: Qn
  nor nor_1 (nor_1_out, clock_1_out, t_ff_2_q, t_ff_1_q);
  D_Flip_Flop d_ff_4 (
    .clk(clock_1_out), .D(d_ff_3_q), .Q(d_ff_4_q), .preset(nor_1_out), .en(1'b1), .reset(1'b0));  // open: Qn
  not not_1 (not_1_out, clock_1_out);
  and and_1 (and_1_out, d_ff_1_q, ~d_ff_2_q, ~d_ff_3_q, d_ff_4_q);  // AND_Gate
  D_Flip_Flop d_ff_5 (.clk(not_1_out), .D(and_1_out), .Q(out_2), .preset(1'b0), .en(1'b1), .reset(1'b0));  // open: Qn
endmodule
