// Logisim project Guia12.circ as structural Verilog: 5 circuits, main circuit Exe04 Reg.Dir. 6Bits
module Exe01_Reg_Esq_6Bits (
  input  DATA,
  input  CLR,
  output A,
  output B,
  output C,
  output D,
  output E,
  output F
);

  wire CLK_out;

  Clock CLK (.out(CLK_out));
  D_Flip_Flop d_ff_1 (.clk(CLK_out), .D(B), .Q(A), .reset(CLR));  // open: Qn, preset, en
  D_Flip_Flop d_ff_2 (.clk(CLK_out), .D(C), .Q(B), .reset(CLR));  // open: Qn, preset, en
  D_Flip_Flop d_ff_3 (.clk(CLK_out), .D(D), .Q(C), .reset(CLR));  // open: Qn, preset, en
  D_Flip_Flop d_ff_4 (.clk(CLK_out), .D(E), .Q(D), .reset(CLR));  // open: Qn, preset, en
  D_Flip_Flop d_ff_5 (.clk(CLK_out), .D(F), .Q(E), .reset(CLR));  // open: Qn, preset, en
  D_Flip_Flop d_ff_6 (.clk(CLK_out), .D(DATA), .Q(F), .reset(CLR));  // open: Qn, preset, en

  // Notes on the sheet:
  //   Bruno César Lopes Silva - 415985
endmodule

module Exe02_Conv_Paral_Serie_3Bits (
  input  CLR,
  input  LD,
  input  d2,
  input  d1,
  input  d0,
  output A,
  output B,
  output C
);

  wire and_1_out, and_2_out, and_3_out, CLK_out;

  Clock CLK (.out(CLK_out));
  and and_1 (and_1_out, LD, d2);
  D_Flip_Flop d_ff_1 (.clk(CLK_out), .D(1'b0), .Q(A), .preset(and_1_out), .reset(CLR));  // open: Qn, en
  and and_2 (and_2_out, LD, d1);
  D_Flip_Flop d_ff_2 (.clk(CLK_out), .D(A), .Q(B), .preset(and_2_out), .reset(CLR));  // open: Qn, en
  D_Flip_Flop d_ff_3 (.clk(CLK_out), .D(B), .Q(C), .preset(and_3_out), .reset(CLR));  // open: Qn, en
  and and_3 (and_3_out, LD, d0);

  // Notes on the sheet:
  //   Bruno César Lopes Silva - 415985
endmodule

module Exe03_Cont_Dec_5Bits (
  input  CLR,
  output A,
  output B,
  output C,
  output C_2,
  output C_3
);

  wire CLK_out;

  Clock CLK (.out(CLK_out));
  J_K_Flip_Flop j_k_ff_1 (.J(1'b1), .clk(B), .K(1'b1), .Qn(A), .reset(CLR));  // open: Q, preset, en
  J_K_Flip_Flop j_k_ff_2 (.J(1'b1), .clk(C), .K(1'b1), .Qn(B), .reset(CLR));  // open: Q, preset, en
  J_K_Flip_Flop j_k_ff_3 (.J(1'b1), .clk(C_2), .K(1'b1), .Qn(C), .reset(CLR));  // open: Q, preset, en
  J_K_Flip_Flop j_k_ff_4 (.J(1'b1), .clk(C_3), .K(1'b1), .Qn(C_2), .reset(CLR));  // open: Q, preset, en
  J_K_Flip_Flop j_k_ff_5 (.J(1'b1), .clk(CLK_out), .K(1'b1), .Qn(C_3), .reset(CLR));  // open: Q, preset, en

  // Notes on the sheet:
  //   Bruno César Lopes Silva - 415985
endmodule

module Exe04_Reg_Dir__6Bits (
  input  DATA,
  input  CLR,
  output A,
  output B,
  output C,
  output D,
  output E,
  output F
);

  wire CLK_out;

  Clock CLK (.out(CLK_out));
  D_Flip_Flop d_ff_1 (.clk(CLK_out), .D(DATA), .Q(A), .reset(CLR));  // open: Qn, preset, en
  D_Flip_Flop d_ff_2 (.clk(CLK_out), .D(A), .Q(B), .reset(CLR));  // open: Qn, preset, en
  D_Flip_Flop d_ff_3 (.clk(CLK_out), .D(B), .Q(C), .reset(CLR));  // open: Qn, preset, en
  D_Flip_Flop d_ff_4 (.clk(CLK_out), .D(C), .Q(D), .reset(CLR));  // open: Qn, preset, en
  D_Flip_Flop d_ff_5 (.clk(CLK_out), .D(D), .Q(E), .reset(CLR));  // open: Qn, preset, en
  D_Flip_Flop d_ff_6 (.clk(CLK_out), .D(E), .Q(F), .reset(CLR));  // open: Qn, preset, en

  // Notes on the sheet:
  //   Bruno César Lopes Silva - 415985
endmodule

module Exe05_Cont_Cresc__5Bits (
  input  CLR,
  output A,
  output B,
  output C,
  output D,
  output E
);

  wire CLK_out, j_k_ff_2_q, j_k_ff_3_q, j_k_ff_4_q, j_k_ff_5_q;

  Clock CLK (.out(CLK_out));
  J_K_Flip_Flop j_k_ff_1 (.J(1'b1), .clk(j_k_ff_2_q), .K(1'b1), .Qn(A), .reset(CLR));  // open: Q, preset, en
  J_K_Flip_Flop j_k_ff_2 (
    .J(1'b1), .clk(j_k_ff_3_q), .K(1'b1), .Q(j_k_ff_2_q), .Qn(B), .reset(CLR));  // open: preset, en
  J_K_Flip_Flop j_k_ff_3 (
    .J(1'b1), .clk(j_k_ff_4_q), .K(1'b1), .Q(j_k_ff_3_q), .Qn(C), .reset(CLR));  // open: preset, en
  J_K_Flip_Flop j_k_ff_4 (
    .J(1'b1), .clk(j_k_ff_5_q), .K(1'b1), .Q(j_k_ff_4_q), .Qn(D), .reset(CLR));  // open: preset, en
  J_K_Flip_Flop j_k_ff_5 (.J(1'b1), .clk(CLK_out), .K(1'b1), .Q(j_k_ff_5_q), .Qn(E), .reset(CLR));  // open: preset, en

  // Notes on the sheet:
  //   Bruno César Lopes Silva - 415985
endmodule
