// Logisim project Exercicio 2.circ as structural Verilog: 1 circuit, main circuit Guia_11_Ex_02
module Guia_11_Ex_02 (
  input  clear,
  input  load,
  input  data2,
  input  data1,
  input  data0,
  output out_6,
  output out_7,
  output out_8
);

  wire and_1_out, and_2_out, and_3_out, clock_out;

  Clock #(.highDuration(1), .lowDuration(1)) clock (.out(clock_out));
  and and_1 (and_1_out, load, data0);
  D_Flip_Flop #(.trigger("rising")) d_ff_1 (
    .clk(clock_out), .D(1'b0), .Q(out_6), .preset(and_1_out), .reset(clear));  // open: Qn, en
  and and_2 (and_2_out, load, data0);
  D_Flip_Flop #(.trigger("rising")) d_ff_2 (
    .clk(clock_out), .D(out_6), .Q(out_7), .preset(and_2_out), .reset(clear));  // open: Qn, en
  and and_3 (and_3_out, load, data0);
  D_Flip_Flop #(.trigger("rising")) d_ff_3 (
    .clk(clock_out), .D(out_7), .Q(out_8), .preset(and_3_out), .reset(clear));  // open: Qn, en

  assign data1 = data0;
  assign data2 = data0;

  // Notes on the sheet:
  //   Nome: Bruno Rafael Nicolletti - Matrícula: 380752
  //   constant
endmodule
