// Logisim project Exercicio 3.circ as structural Verilog: 1 circuit, main circuit Guia_11_Ex_03
module Guia_11_Ex_03 (
  input  clear,
  output out_2,
  output out_3,
  output out_4,
  output out_5,
  output out_6
);

  wire clock_out, j_k_ff_2_q, j_k_ff_3_q, j_k_ff_4_q, j_k_ff_5_q;

  Clock #(.highDuration(1), .lowDuration(1)) clock (.out(clock_out));
  J_K_Flip_Flop #(.trigger("rising")) j_k_ff_1 (
    .J(1'b1), .clk(j_k_ff_2_q), .K(1'b1), .Qn(out_2), .reset(clear));  // open: Q, preset, en
  J_K_Flip_Flop #(.trigger("rising")) j_k_ff_2 (
    .J(1'b1), .clk(j_k_ff_3_q), .K(1'b1), .Q(j_k_ff_2_q), .Qn(out_3), .reset(clear));  // open: preset, en
  J_K_Flip_Flop #(.trigger("rising")) j_k_ff_3 (
    .J(1'b1), .clk(j_k_ff_4_q), .K(1'b1), .Q(j_k_ff_3_q), .Qn(out_4), .reset(clear));  // open: preset, en
  J_K_Flip_Flop #(.trigger("rising")) j_k_ff_4 (
    .J(1'b1), .clk(j_k_ff_5_q), .K(1'b1), .Q(j_k_ff_4_q), .Qn(out_5), .reset(clear));  // open: preset, en
  J_K_Flip_Flop #(.trigger("rising")) j_k_ff_5 (
    .J(1'b1), .clk(clock_out), .K(1'b1), .Q(j_k_ff_5_q), .Qn(out_6), .reset(clear));  // open: preset, en

  // Notes on the sheet:
  //   constant
  //   Nome: Bruno Rafael Nicolletti - Matrícula: 380752
endmodule
