// Logisim project Guia11Ex02.circ as structural Verilog: 1 circuit, main circuit Ex02
module Ex02 (
  input  CLR,
  input  LD,
  input  d1,
  input  d0,
  input  d2,
  output A,
  output B,
  output C
);

  wire and_1_out, and_2_out, and_3_out, CLK_out;

  Clock CLK (.out(CLK_out));
  and and_1 (and_1_out, LD, d2);
  D_Flip_Flop d_ff_1 (.clk(CLK_out), .D(1'b0), .Q(A), .preset(and_1_out), .reset(CLR));  // open: Qn, en
  D_Flip_Flop d_ff_2 (.clk(CLK_out), .D(A), .Q(B), .preset(and_2_out), .reset(CLR));  // open: Qn, en
  and and_2 (and_2_out, LD, d1);
  D_Flip_Flop d_ff_3 (.clk(CLK_out), .D(B), .Q(C), .preset(and_3_out), .reset(CLR));  // open: Qn, en
  and and_3 (and_3_out, LD, d0);

  // Notes on the sheet:
  //   Álvaro Henrique de Araujo Rungue - 395487 ( Guia 11 EX 02 )  
endmodule
