// Logisim project Guia11Ex04.circ as structural Verilog: 1 circuit, main circuit Ex04
module Ex04 (
  input  DATA,
  input  CLR,
  output A,
  output B,
  output C,
  output D,
  output E,
  output F
);

  wire CLK_out;

  Clock CLK (.out(CLK_out));
  D_Flip_Flop d_ff_1 (.clk(CLK_out), .D(DATA), .Q(A), .reset(CLR));  // open: Qn, preset, en
  D_Flip_Flop d_ff_2 (.clk(CLK_out), .D(A), .Q(B), .reset(CLR));  // open: Qn, preset, en
  D_Flip_Flop d_ff_3 (.clk(CLK_out), .D(E), .Q(F), .reset(CLR));  // open: Qn, preset, en
  D_Flip_Flop d_ff_4 (.clk(CLK_out), .D(B), .Q(C), .reset(CLR));  // open: Qn, preset, en
  D_Flip_Flop d_ff_5 (.clk(CLK_out), .D(C), .Q(D), .reset(CLR));  // open: Qn, preset, en
  D_Flip_Flop d_ff_6 (.clk(CLK_out), .D(D), .Q(E), .reset(CLR));  // open: Qn, preset, en

  // Notes on the sheet:
  //   Álvaro Henrique de Araujo Rungue - 395487 ( Guia 11 EX 04 ) 
endmodule
