// Logisim project guia11_03.circ as structural Verilog: 1 circuit, main circuit guia11_03
module guia11_03 (
  input  CLR,
  output A,
  output B,
  output C,
  output C_2,
  output C_3
);

  wire CLK_out;

  Clock CLK (.out(CLK_out));
  J_K_Flip_Flop j_k_ff_1 (.J(1'b1), .clk(B), .K(1'b1), .Qn(A), .reset(CLR));  // open: Q, preset, en
  J_K_Flip_Flop j_k_ff_2 (.J(1'b1), .clk(C), .K(1'b1), .Qn(B), .reset(CLR));  // open: Q, preset, en
  J_K_Flip_Flop j_k_ff_3 (.J(1'b1), .clk(C_2), .K(1'b1), .Qn(C), .reset(CLR));  // open: Q, preset, en
  J_K_Flip_Flop j_k_ff_4 (.J(1'b1), .clk(C_3), .K(1'b1), .Qn(C_2), .reset(CLR));  // open: Q, preset, en
  J_K_Flip_Flop j_k_ff_5 (.J(1'b1), .clk(CLK_out), .K(1'b1), .Qn(C_3), .reset(CLR));  // open: Q, preset, en

  // Notes on the sheet:
  //   396673 - Anderson Belchior de Carvalho
  //   Implementar um contador de pulsos assíncrono decrescente com 05 bits.
endmodule
