// Logisim project guia11_05.circ as structural Verilog: 1 circuit, main circuit guia11_05
module guia11_05 (
  input  CLR,
  output A,
  output B,
  output C,
  output D,
  output E
);

  wire CLK_out, j_k_ff_2_q, j_k_ff_3_q, j_k_ff_4_q, j_k_ff_5_q;

  Clock CLK (.out(CLK_out));
  J_K_Flip_Flop j_k_ff_1 (.J(1'b1), .clk(j_k_ff_2_q), .K(1'b1), .Qn(A), .reset(CLR));  // open: Q, preset, en
  J_K_Flip_Flop j_k_ff_2 (
    .J(1'b1), .clk(j_k_ff_3_q), .K(1'b1), .Q(j_k_ff_2_q), .Qn(B), .reset(CLR));  // open: preset, en
  J_K_Flip_Flop j_k_ff_3 (
    .J(1'b1), .clk(j_k_ff_4_q), .K(1'b1), .Q(j_k_ff_3_q), .Qn(C), .reset(CLR));  // open: preset, en
  J_K_Flip_Flop j_k_ff_4 (
    .J(1'b1), .clk(j_k_ff_5_q), .K(1'b1), .Q(j_k_ff_4_q), .Qn(D), .reset(CLR));  // open: preset, en
  J_K_Flip_Flop j_k_ff_5 (.J(1'b1), .clk(CLK_out), .K(1'b1), .Q(j_k_ff_5_q), .Qn(E), .reset(CLR));  // open: preset, en

  // Notes on the sheet:
  //   396673 - Anderson Belchior de Carvalho
  //   Implementar um contador de pulsos assíncrono crescente com 05 bits.
endmodule
