// Logisim project Guia11.circ as structural Verilog
module ex01 (
  input  DT,
  input  CLR,
  output a,
  output b,
  output c,
  output d,
  output e,
  output f
);

  wire CLCK_out;

  Clock CLCK (.out(CLCK_out));
  D_Flip_Flop d_ff_1 (.clk(CLCK_out), .D(b), .Q(a), .preset(CLR));  // open: Qn, en, reset
  D_Flip_Flop d_ff_2 (.clk(CLCK_out), .D(c), .Q(b), .preset(CLR));  // open: Qn, en, reset
  D_Flip_Flop d_ff_3 (.clk(CLCK_out), .D(d), .Q(c), .preset(CLR));  // open: Qn, en, reset
  D_Flip_Flop d_ff_4 (.clk(CLCK_out), .D(e), .Q(d), .preset(CLR));  // open: Qn, en, reset
  D_Flip_Flop d_ff_5 (.clk(CLCK_out), .D(f), .Q(e), .preset(CLR));  // open: Qn, en, reset
  D_Flip_Flop d_ff_6 (.clk(CLCK_out), .D(DT), .Q(f), .preset(CLR));  // open: Qn, en, reset

  // Notes on the sheet:
  //   Karen Alves Pereira - 407451
endmodule

module ex02 (
  input  CLR,
  input  LD,
  input  in_3,
  input  in_4,
  input  in_5,
  output a,
  output b,
  output c,
  output out_9
);

  wire and_1_out, and_2_out, and_3_out;

  Clock CLCK (.out(out_9));
  D_Flip_Flop d_ff_1 (.clk(out_9), .D(1'b0), .Q(a), .preset(CLR), .reset(and_1_out));  // open: Qn, en
  and and_1 (and_1_out, LD, in_3);
  D_Flip_Flop d_ff_2 (.clk(out_9), .D(a), .Q(b), .preset(CLR), .reset(and_2_out));  // open: Qn, en
  and and_2 (and_2_out, LD, in_4);
  D_Flip_Flop d_ff_3 (.clk(out_9), .D(b), .Q(c), .preset(CLR), .reset(and_3_out));  // open: Qn, en
  and and_3 (and_3_out, LD, in_5);

  // Notes on the sheet:
  //   Karen Alves Pereira - 407451
endmodule

module ex03 (
  input  CLR,
  output a,
  output b,
  output c,
  output d,
  output e
);

  wire CLCK_out, j_k_ff_2_q, j_k_ff_3_q, j_k_ff_4_q, j_k_ff_5_q;

  Clock CLCK (.out(CLCK_out));
  J_K_Flip_Flop j_k_ff_1 (.J(1'b1), .clk(j_k_ff_2_q), .K(1'b1), .Q(a), .reset(CLR));  // open: Qn, preset, en
  J_K_Flip_Flop j_k_ff_2 (
    .J(1'b1), .clk(j_k_ff_3_q), .K(1'b1), .Q(j_k_ff_2_q), .Qn(b), .reset(CLR));  // open: preset, en
  J_K_Flip_Flop j_k_ff_3 (
    .J(1'b1), .clk(j_k_ff_4_q), .K(1'b1), .Q(j_k_ff_3_q), .Qn(c), .reset(CLR));  // open: preset, en
  J_K_Flip_Flop j_k_ff_4 (.clk(j_k_ff_5_q), .Q(j_k_ff_4_q), .Qn(d), .reset(CLR));  // open: J, K, preset, en
  J_K_Flip_Flop j_k_ff_5 (.clk(CLCK_out), .Q(j_k_ff_5_q), .Qn(e), .reset(CLR));  // open: J, K, preset, en

  // Notes on the sheet:
  //   Karen Alves Pereira - 407451
endmodule

module ex04 (
  input  DT,
  input  CLR,
  output a,
  output b,
  output c,
  output d,
  output e,
  output f
);

  wire CLCK_out;

  Clock CLCK (.out(CLCK_out));
  D_Flip_Flop d_ff_1 (.clk(CLCK_out), .D(DT), .Q(a), .preset(CLR));  // open: Qn, en, reset
  D_Flip_Flop d_ff_2 (.clk(CLCK_out), .D(a), .Q(b), .preset(CLR));  // open: Qn, en, reset
  D_Flip_Flop d_ff_3 (.clk(CLCK_out), .D(b), .Q(c), .preset(CLR));  // open: Qn, en, reset
  D_Flip_Flop d_ff_4 (.clk(CLCK_out), .D(c), .Q(d), .preset(CLR));  // open: Qn, en, reset
  D_Flip_Flop d_ff_5 (.clk(CLCK_out), .D(d), .Q(e), .preset(CLR));  // open: Qn, en, reset
  D_Flip_Flop d_ff_6 (.clk(CLCK_out), .Q(f), .preset(CLR));  // open: D, Qn, en, reset

  // Notes on the sheet:
  //   Karen Alves Pereira - 407451
endmodule
