// Logisim project Guia_11.circ as structural Verilog: 5 circuits, main circuit Exercicio03
module Exercicio01 (
  input  DATA,
  input  CLR,
  output A,
  output B,
  output C,
  output D,
  output E,
  output F
);

  wire CLK_out;

  Clock CLK (.out(CLK_out));
  D_Flip_Flop d_ff_1 (.clk(CLK_out), .D(B), .Q(A), .reset(CLR));  // open: Qn, preset, en
  D_Flip_Flop d_ff_2 (.clk(CLK_out), .D(C), .Q(B), .reset(CLR));  // open: Qn, preset, en
  D_Flip_Flop d_ff_3 (.clk(CLK_out), .D(D), .Q(C), .reset(CLR));  // open: Qn, preset, en
  D_Flip_Flop d_ff_4 (.clk(CLK_out), .D(E), .Q(D), .reset(CLR));  // open: Qn, preset, en
  D_Flip_Flop d_ff_5 (.clk(CLK_out), .D(F), .Q(E), .reset(CLR));  // open: Qn, preset, en
  D_Flip_Flop d_ff_6 (.clk(CLK_out), .D(DATA), .Q(F), .reset(CLR));  // open: Qn, preset, en

  // Notes on the sheet:
  //   Aluno: Alyson Deives Matricula: 416589
endmodule

module Exercicio02 (
  input  CLR,
  input  LD,
  input  d3,
  input  d2,
  input  d0,
  output A,
  output B,
  output C,
  output out_9
);

  wire and_1_out, and_2_out, and_3_out;

  Clock CLK (.out(out_9));
  and and_1 (and_1_out, LD, d3);
  D_Flip_Flop d_ff_1 (.clk(out_9), .D(1'b0), .Q(A), .preset(and_1_out), .reset(CLR));  // open: Qn, en
  and and_2 (and_2_out, LD, d2);
  D_Flip_Flop d_ff_2 (.clk(out_9), .D(A), .Q(B), .preset(and_2_out), .reset(CLR));  // open: Qn, en
  D_Flip_Flop d_ff_3 (.clk(out_9), .D(B), .Q(C), .preset(and_3_out), .reset(CLR));  // open: Qn, en
  and and_3 (and_3_out, LD, d0);

  // Notes on the sheet:
  //   Aluno: Alyson Deives Matricula: 416589
endmodule

module Exercicio03 (
  input  CLR,
  output A,
  output B,
  output C,
  output D,
  output E
);

  wire CLK_out, j_k_ff_2_q, j_k_ff_3_q, j_k_ff_4_q, j_k_ff_5_q;

  Clock CLK (.out(CLK_out));
  J_K_Flip_Flop j_k_ff_1 (.J(1'b1), .clk(j_k_ff_2_q), .K(1'b1), .Qn(A), .reset(CLR));  // open: Q, preset, en
  J_K_Flip_Flop j_k_ff_2 (
    .J(1'b1), .clk(j_k_ff_3_q), .K(1'b1), .Q(j_k_ff_2_q), .Qn(B), .reset(CLR));  // open: preset, en
  J_K_Flip_Flop j_k_ff_3 (
    .J(1'b1), .clk(j_k_ff_4_q), .K(1'b1), .Q(j_k_ff_3_q), .Qn(C), .reset(CLR));  // open: preset, en
  J_K_Flip_Flop j_k_ff_4 (.clk(j_k_ff_5_q), .Q(j_k_ff_4_q), .Qn(D), .reset(CLR));  // open: J, K, preset, en
  J_K_Flip_Flop j_k_ff_5 (.clk(CLK_out), .Q(j_k_ff_5_q), .Qn(E), .reset(CLR));  // open: J, K, preset, en

  // Notes on the sheet:
  //   Aluno: Alyson Deives Matricula: 416589
endmodule

module Exercicio04 (
  input  DATA,
  input  CLR,
  output A,
  output B,
  output C,
  output D,
  output E,
  output F
);

  wire CLK_out;

  Clock CLK (.out(CLK_out));
  D_Flip_Flop d_ff_1 (.clk(CLK_out), .D(DATA), .Q(A), .reset(CLR));  // open: Qn, preset, en
  D_Flip_Flop d_ff_2 (.clk(CLK_out), .D(A), .Q(B), .reset(CLR));  // open: Qn, preset, en
  D_Flip_Flop d_ff_3 (.clk(CLK_out), .D(B), .Q(C), .reset(CLR));  // open: Qn, preset, en
  D_Flip_Flop d_ff_4 (.clk(CLK_out), .D(C), .Q(D), .reset(CLR));  // open: Qn, preset, en
  D_Flip_Flop d_ff_5 (.clk(CLK_out), .D(D), .Q(E), .reset(CLR));  // open: Qn, preset, en
  D_Flip_Flop d_ff_6 (.clk(CLK_out), .Q(F), .reset(CLR));  // open: D, Qn, preset, en

  // Notes on the sheet:
  //   Aluno: Alyson Deives Matricula: 416589
endmodule

module Exercicio05 (
  input  CLR,
  output A,
  output B,
  output C,
  output out_5,
  output out_6
);

  wire CLK_out, j_k_ff_2_q, j_k_ff_3_q, j_k_ff_4_q, j_k_ff_5_q;

  Clock CLK (.out(CLK_out));
  J_K_Flip_Flop j_k_ff_1 (.J(1'b1), .clk(j_k_ff_2_q), .K(1'b1), .Qn(A), .reset(CLR));  // open: Q, preset, en
  J_K_Flip_Flop j_k_ff_2 (
    .J(1'b1), .clk(j_k_ff_3_q), .K(1'b1), .Q(j_k_ff_2_q), .Qn(B), .reset(CLR));  // open: preset, en
  J_K_Flip_Flop j_k_ff_3 (
    .J(1'b1), .clk(j_k_ff_4_q), .K(1'b1), .Q(j_k_ff_3_q), .Qn(C), .reset(CLR));  // open: preset, en
  J_K_Flip_Flop j_k_ff_4 (
    .J(1'b1), .clk(j_k_ff_5_q), .K(1'b1), .Q(j_k_ff_4_q), .Qn(out_5), .reset(CLR));  // open: preset, en
  J_K_Flip_Flop j_k_ff_5 (
    .J(1'b1), .clk(CLK_out), .K(1'b1), .Q(j_k_ff_5_q), .Qn(out_6), .reset(CLR));  // open: preset, en

  // Notes on the sheet:
  //   Aluno: Alyson Deives Matricula: 416589
endmodule
