// Logisim project GUIA11 AC.circ as structural Verilog: 5 circuits, main circuit guia11exercicio01
module guia11exercicio01 (
  input  Input,
  input  Clear,
  output [5:0] s
);

  wire Clock_out;

  Clock Clock (.out(Clock_out));
  D_Flip_Flop d_ff_1 (.clk(Clock_out), .D(Input), .Q(s[5]), .reset(Clear));  // open: Qn, preset, en
  D_Flip_Flop d_ff_2 (.clk(Clock_out), .D(s[5]), .Q(s[4]), .reset(Clear));  // open: Qn, preset, en
  D_Flip_Flop d_ff_3 (.clk(Clock_out), .D(s[4]), .Q(s[3]), .reset(Clear));  // open: Qn, preset, en
  D_Flip_Flop d_ff_4 (.clk(Clock_out), .D(s[3]), .Q(s[2]), .reset(Clear));  // open: Qn, preset, en
  D_Flip_Flop d_ff_5 (.clk(Clock_out), .D(s[2]), .Q(s[1]), .reset(Clear));  // open: Qn, preset, en
  D_Flip_Flop d_ff_6 (.clk(Clock_out), .D(s[1]), .Q(s[0]), .reset(Clear));  // open: Qn, preset, en

  // Notes on the sheet:
  //   LUIZ MARQUES DE OLIVEIRA - 417138
  //   Deslocador de bits para esquerda .
endmodule

module guia11exercicio02 (
  input  In,
  input  Clear,
  input  EnLoads,
  input  [1:0] Loads
);

  wire and_1_out, and_2_out, Clock_out, j_k_ff_1_q, j_k_ff_1_qn, not_1_out;

  Clock Clock (.out(Clock_out));
  not not_1 (not_1_out, In);
  J_K_Flip_Flop j_k_ff_1 (
    .J(In), .clk(Clock_out), .K(not_1_out), .Q(j_k_ff_1_q), .Qn(j_k_ff_1_qn), .preset(and_1_out),
    .reset(Clear));  // open: en
  and and_1 (and_1_out, Loads[1], EnLoads);
  J_K_Flip_Flop j_k_ff_2 (
    .J(j_k_ff_1_q), .clk(Clock_out), .K(j_k_ff_1_qn), .preset(and_2_out), .reset(Clear));  // open: Q, Qn, en
  and and_2 (and_2_out, EnLoads, Loads[0]);

  // Notes on the sheet:
  //   LUIZ MARQUES DE OLIVEIRA - 417138
  //   Conversor Paralelo-Serie
endmodule

module guia11exercicio03 (
  input  Reset
);

  wire Clock_out, j_k_ff_2_q, j_k_ff_3_q, j_k_ff_4_q, j_k_ff_5_q;

  J_K_Flip_Flop j_k_ff_1 (.J(1'b1), .clk(j_k_ff_2_q), .K(1'b1), .reset(Reset));  // open: Q, Qn, preset, en
  J_K_Flip_Flop j_k_ff_2 (.J(1'b1), .clk(j_k_ff_3_q), .K(1'b1), .Q(j_k_ff_2_q), .reset(Reset));  // open: Qn, preset, en
  J_K_Flip_Flop j_k_ff_3 (.J(1'b1), .clk(j_k_ff_4_q), .K(1'b1), .Q(j_k_ff_3_q), .reset(Reset));  // open: Qn, preset, en
  J_K_Flip_Flop j_k_ff_4 (.J(1'b1), .clk(j_k_ff_5_q), .K(1'b1), .Q(j_k_ff_4_q), .reset(Reset));  // open: Qn, preset, en
  J_K_Flip_Flop j_k_ff_5 (.J(1'b1), .clk(Clock_out), .K(1'b1), .Q(j_k_ff_5_q), .reset(Reset));  // open: Qn, preset, en
  Clock Clock (.out(Clock_out));

  // Notes on the sheet:
  //   Pulsos Decrescentes
  //   LUIZ MARQUES DE OLIVEIRA - 417138
endmodule

module guia11exercicio04 (
  input  Input,
  input  Clear,
  output [4:0] s
);

  wire Clock_out;

  Clock Clock (.out(Clock_out));
  D_Flip_Flop d_ff_1 (.clk(Clock_out), .D(Input), .Q(s[4]), .reset(Clear));  // open: Qn, preset, en
  D_Flip_Flop d_ff_2 (.clk(Clock_out), .D(s[4]), .Q(s[3]), .reset(Clear));  // open: Qn, preset, en
  D_Flip_Flop d_ff_3 (.clk(Clock_out), .D(s[3]), .Q(s[2]), .reset(Clear));  // open: Qn, preset, en
  D_Flip_Flop d_ff_4 (.clk(Clock_out), .D(s[2]), .Q(s[1]), .reset(Clear));  // open: Qn, preset, en
  D_Flip_Flop d_ff_5 (.clk(Clock_out), .D(s[1]), .Q(s[0]), .reset(Clear));  // open: Qn, preset, en

  // Notes on the sheet:
  //   LUIZ MARQUES DE OLIVEIRA - 417138
  //   Deslocador de bits para a direita .
endmodule

module guia11exercicio05 (
  input  Reset
);

  wire Clock_out, j_k_ff_2_qn, j_k_ff_3_qn, j_k_ff_4_qn, j_k_ff_5_qn;

  J_K_Flip_Flop j_k_ff_1 (.J(1'b1), .clk(j_k_ff_2_qn), .K(1'b1), .reset(Reset));  // open: Q, Qn, preset, en
  J_K_Flip_Flop j_k_ff_2 (
    .J(1'b1), .clk(j_k_ff_3_qn), .K(1'b1), .Qn(j_k_ff_2_qn), .reset(Reset));  // open: Q, preset, en
  J_K_Flip_Flop j_k_ff_3 (
    .J(1'b1), .clk(j_k_ff_4_qn), .K(1'b1), .Qn(j_k_ff_3_qn), .reset(Reset));  // open: Q, preset, en
  J_K_Flip_Flop j_k_ff_4 (
    .J(1'b1), .clk(j_k_ff_5_qn), .K(1'b1), .Qn(j_k_ff_4_qn), .reset(Reset));  // open: Q, preset, en
  J_K_Flip_Flop j_k_ff_5 (.J(1'b1), .clk(Clock_out), .K(1'b1), .Qn(j_k_ff_5_qn), .reset(Reset));  // open: Q, preset, en
  Clock Clock (.out(Clock_out));

  // Notes on the sheet:
  //   LUIZ MARQUES DE OLIVEIRA - 417138
  //   Pulsos Crescentes
endmodule
