// Logisim project Guia_11.circ as structural Verilog: 5 circuits, main circuit Exercicio03
module Exercicio01 (
  input  DATA,
  input  CLR,
  output a,
  output b,
  output c,
  output d,
  output e,
  output f
);

  wire CLK_out;

  Clock CLK (.out(CLK_out));
  D_Flip_Flop d_ff_1 (.clk(CLK_out), .D(b), .Q(a), .reset(CLR));  // open: Qn, preset, en
  D_Flip_Flop d_ff_2 (.clk(CLK_out), .D(c), .Q(b), .reset(CLR));  // open: Qn, preset, en
  D_Flip_Flop d_ff_3 (.clk(CLK_out), .D(d), .Q(c), .reset(CLR));  // open: Qn, preset, en
  D_Flip_Flop d_ff_4 (.clk(CLK_out), .D(e), .Q(d), .reset(CLR));  // open: Qn, preset, en
  D_Flip_Flop d_ff_5 (.clk(CLK_out), .D(DATA), .Q(e), .reset(CLR));  // open: Qn, preset, en
  D_Flip_Flop d_ff_6 (.clk(CLK_out), .Q(f), .reset(CLR));  // open: D, Qn, preset, en

  // Notes on the sheet:
  //   Raphaela Fernanda Silva - 420141
endmodule

module Exercicio02 (
  input  CLR,
  input  LD,
  input  _4,
  input  _3,
  input  _2,
  output a,
  output b,
  output c,
  output out_9
);

  wire and_1_out, and_2_out, and_3_out;

  Clock CLK (.out(out_9));
  and and_1 (and_1_out, LD, _4);
  D_Flip_Flop d_ff_1 (.clk(out_9), .D(1'b0), .Q(a), .preset(and_1_out), .reset(CLR));  // open: Qn, en
  and and_2 (and_2_out, LD, _3);
  D_Flip_Flop d_ff_2 (.clk(out_9), .D(a), .Q(b), .preset(and_2_out), .reset(CLR));  // open: Qn, en
  D_Flip_Flop d_ff_3 (.clk(out_9), .D(b), .Q(c), .preset(and_3_out), .reset(CLR));  // open: Qn, en
  and and_3 (and_3_out, LD, _2);

  // Notes on the sheet:
  //   Raphaela Fernanda Silva - 420141
endmodule

module Exercicio03 (
  input  CLR,
  output a,
  output b,
  output c,
  output d,
  output e
);

  wire CLK_out, j_k_ff_2_q, j_k_ff_3_q, j_k_ff_4_q, j_k_ff_5_q;

  Clock CLK (.out(CLK_out));
  J_K_Flip_Flop j_k_ff_1 (.J(1'b1), .clk(j_k_ff_2_q), .K(1'b1), .Qn(a), .reset(CLR));  // open: Q, preset, en
  J_K_Flip_Flop j_k_ff_2 (
    .J(1'b1), .clk(j_k_ff_3_q), .K(1'b1), .Q(j_k_ff_2_q), .Qn(b), .reset(CLR));  // open: preset, en
  J_K_Flip_Flop j_k_ff_3 (
    .J(1'b1), .clk(j_k_ff_4_q), .K(1'b1), .Q(j_k_ff_3_q), .Qn(c), .reset(CLR));  // open: preset, en
  J_K_Flip_Flop j_k_ff_4 (.clk(j_k_ff_5_q), .Q(j_k_ff_4_q), .Qn(d), .reset(CLR));  // open: J, K, preset, en
  J_K_Flip_Flop j_k_ff_5 (.clk(CLK_out), .Q(j_k_ff_5_q), .Qn(e), .reset(CLR));  // open: J, K, preset, en

  // Notes on the sheet:
  //   Raphaela Fernanda Silva - 420141
endmodule

module Exercicio04 (
  input  DATA,
  input  CLR,
  output a,
  output b,
  output c,
  output d,
  output e,
  output f
);

  wire CLK_out;

  Clock CLK (.out(CLK_out));
  D_Flip_Flop d_ff_1 (.clk(CLK_out), .D(DATA), .Q(a), .reset(CLR));  // open: Qn, preset, en
  D_Flip_Flop d_ff_2 (.clk(CLK_out), .D(a), .Q(b), .reset(CLR));  // open: Qn, preset, en
  D_Flip_Flop d_ff_3 (.clk(CLK_out), .D(b), .Q(c), .reset(CLR));  // open: Qn, preset, en
  D_Flip_Flop d_ff_4 (.clk(CLK_out), .D(c), .Q(d), .reset(CLR));  // open: Qn, preset, en
  D_Flip_Flop d_ff_5 (.clk(CLK_out), .D(d), .Q(e), .reset(CLR));  // open: Qn, preset, en
  D_Flip_Flop d_ff_6 (.clk(CLK_out), .Q(f), .reset(CLR));  // open: D, Qn, preset, en

  // Notes on the sheet:
  //   Raphaela Fernanda Silva - 420141
endmodule

module Exercicio05 (
  input  CLR,
  output a,
  output b,
  output c,
  output d,
  output out_6
);

  wire CLK_out, j_k_ff_2_q, j_k_ff_3_q, j_k_ff_4_q, j_k_ff_5_q;

  Clock CLK (.out(CLK_out));
  J_K_Flip_Flop j_k_ff_1 (.J(1'b1), .clk(j_k_ff_2_q), .K(1'b1), .Qn(a), .reset(CLR));  // open: Q, preset, en
  J_K_Flip_Flop j_k_ff_2 (
    .J(1'b1), .clk(j_k_ff_3_q), .K(1'b1), .Q(j_k_ff_2_q), .Qn(b), .reset(CLR));  // open: preset, en
  J_K_Flip_Flop j_k_ff_3 (
    .J(1'b1), .clk(j_k_ff_4_q), .K(1'b1), .Q(j_k_ff_3_q), .Qn(c), .reset(CLR));  // open: preset, en
  J_K_Flip_Flop j_k_ff_4 (
    .J(1'b1), .clk(j_k_ff_5_q), .K(1'b1), .Q(j_k_ff_4_q), .Qn(d), .reset(CLR));  // open: preset, en
  J_K_Flip_Flop j_k_ff_5 (
    .J(1'b1), .clk(CLK_out), .K(1'b1), .Q(j_k_ff_5_q), .Qn(out_6), .reset(CLR));  // open: preset, en

  // Notes on the sheet:
  //   Raphaela Fernanda Silva -420141
endmodule
