// Logisim project guia11.circ as structural Verilog: 5 circuits, main circuit exer01
module exer01 (
  input  Input,
  input  Clear,
  output [5:0] s
);

  wire Clock_out;

  Clock Clock (.out(Clock_out));
  D_Flip_Flop d_ff_1 (.clk(Clock_out), .D(Input), .Q(s[5]), .reset(Clear));  // open: Qn, preset, en
  D_Flip_Flop d_ff_2 (.clk(Clock_out), .D(s[5]), .Q(s[4]), .reset(Clear));  // open: Qn, preset, en
  D_Flip_Flop d_ff_3 (.clk(Clock_out), .D(s[3]), .Q(s[2]), .reset(Clear));  // open: Qn, preset, en
  D_Flip_Flop d_ff_4 (.clk(Clock_out), .D(s[4]), .Q(s[3]), .reset(Clear));  // open: Qn, preset, en
  D_Flip_Flop d_ff_5 (.clk(Clock_out), .D(s[2]), .Q(s[1]), .reset(Clear));  // open: Qn, preset, en
  D_Flip_Flop d_ff_6 (.clk(Clock_out), .D(s[1]), .Q(s[0]), .reset(Clear));  // open: Qn, preset, en

  // Notes on the sheet:
  //   Thaise Souto Martins - 395504
endmodule

module exer02 (
  input  Input,
  input  Clear,
  output [5:0] s
);

  wire Clock_out;

  Clock Clock (.out(Clock_out));
  D_Flip_Flop d_ff_1 (.clk(Clock_out), .D(Input), .Q(s[5]), .reset(Clear));  // open: Qn, preset, en
  D_Flip_Flop d_ff_2 (.clk(Clock_out), .D(s[5]), .Q(s[4]), .reset(Clear));  // open: Qn, preset, en
  D_Flip_Flop d_ff_3 (.clk(Clock_out), .D(s[4]), .Q(s[3]), .reset(Clear));  // open: Qn, preset, en
  D_Flip_Flop d_ff_4 (.clk(Clock_out), .D(s[3]), .Q(s[2]), .reset(Clear));  // open: Qn, preset, en
  D_Flip_Flop d_ff_5 (.clk(Clock_out), .D(s[2]), .Q(s[1]), .reset(Clear));  // open: Qn, preset, en
  D_Flip_Flop d_ff_6 (.clk(Clock_out), .D(s[1]), .Q(s[0]), .reset(Clear));  // open: Qn, preset, en

  // Notes on the sheet:
  //   Thaise Souto Martins - 395504
endmodule

module exer03 (
  input  Input,
  input  Clear,
  output [5:0] s
);

  wire Clock_out;

  Clock Clock (.out(Clock_out));
  D_Flip_Flop d_ff_1 (.clk(Clock_out), .D(Input), .Q(s[5]), .reset(Clear));  // open: Qn, preset, en
  D_Flip_Flop d_ff_2 (.clk(Clock_out), .D(s[5]), .Q(s[4]), .reset(Clear));  // open: Qn, preset, en
  D_Flip_Flop d_ff_3 (.clk(Clock_out), .D(s[4]), .Q(s[3]), .reset(Clear));  // open: Qn, preset, en
  D_Flip_Flop d_ff_4 (.clk(Clock_out), .D(s[3]), .Q(s[2]), .reset(Clear));  // open: Qn, preset, en
  D_Flip_Flop d_ff_5 (.clk(Clock_out), .D(s[2]), .Q(s[1]), .reset(Clear));  // open: Qn, preset, en
  D_Flip_Flop d_ff_6 (.clk(Clock_out), .D(s[1]), .Q(s[0]), .reset(Clear));  // open: Qn, preset, en

  // Notes on the sheet:
  //   Thaise Souto Martins - 395504
endmodule

module exer04 (
  input  Input,
  input  Clear,
  output [5:0] s
);

  wire Clock_out;

  Clock Clock (.out(Clock_out));
  D_Flip_Flop d_ff_1 (.clk(Clock_out), .D(Input), .Q(s[5]), .reset(Clear));  // open: Qn, preset, en
  D_Flip_Flop d_ff_2 (.clk(Clock_out), .D(s[5]), .Q(s[4]), .reset(Clear));  // open: Qn, preset, en
  D_Flip_Flop d_ff_3 (.clk(Clock_out), .D(s[3]), .Q(s[2]), .reset(Clear));  // open: Qn, preset, en
  D_Flip_Flop d_ff_4 (.clk(Clock_out), .D(s[4]), .Q(s[3]), .reset(Clear));  // open: Qn, preset, en
  D_Flip_Flop d_ff_5 (.clk(Clock_out), .D(s[2]), .Q(s[1]), .reset(Clear));  // open: Qn, preset, en
  D_Flip_Flop d_ff_6 (.clk(Clock_out), .D(s[1]), .Q(s[0]), .reset(Clear));  // open: Qn, preset, en

  // Notes on the sheet:
  //   Thaise Souto Martins - 395504
endmodule

module exer05 (
  input  Input,
  input  Clear,
  output [5:0] s
);

  wire Clock_out;

  Clock Clock (.out(Clock_out));
  D_Flip_Flop d_ff_1 (.clk(Clock_out), .D(Input), .Q(s[5]), .reset(Clear));  // open: Qn, preset, en
  D_Flip_Flop d_ff_2 (.clk(Clock_out), .D(s[5]), .Q(s[4]), .reset(Clear));  // open: Qn, preset, en
  D_Flip_Flop d_ff_3 (.clk(Clock_out), .D(s[3]), .Q(s[2]), .reset(Clear));  // open: Qn, preset, en
  D_Flip_Flop d_ff_4 (.clk(Clock_out), .D(s[4]), .Q(s[3]), .reset(Clear));  // open: Qn, preset, en
  D_Flip_Flop d_ff_5 (.clk(Clock_out), .D(s[2]), .Q(s[1]), .reset(Clear));  // open: Qn, preset, en
  D_Flip_Flop d_ff_6 (.clk(Clock_out), .D(s[1]), .Q(s[0]), .reset(Clear));  // open: Qn, preset, en

  // Notes on the sheet:
  //   Thaise Souto Martins - 395504
endmodule
