// Logisim project Guia11.circ as structural Verilog: 5 circuits, main circuit Exercicio1
module Exercicio1 (
  input  Input,
  input  Clear,
  output [5:0] \saída 
);

  wire Clock_out;

  Clock Clock (.out(Clock_out));
  D_Flip_Flop d_ff_1 (.clk(Clock_out), .D(Input), .Q(\saída [5]), .reset(Clear));  // open: Qn, preset, en
  D_Flip_Flop d_ff_2 (.clk(Clock_out), .D(\saída [5]), .Q(\saída [4]), .reset(Clear));  // open: Qn, preset, en
  D_Flip_Flop d_ff_3 (.clk(Clock_out), .D(\saída [4]), .Q(\saída [3]), .reset(Clear));  // open: Qn, preset, en
  D_Flip_Flop d_ff_4 (.clk(Clock_out), .D(\saída [2]), .Q(\saída [1]), .reset(Clear));  // open: Qn, preset, en
  D_Flip_Flop d_ff_5 (.clk(Clock_out), .D(\saída [3]), .Q(\saída [2]), .reset(Clear));  // open: Qn, preset, en
  D_Flip_Flop d_ff_6 (.clk(Clock_out), .D(\saída [1]), .Q(\saída [0]), .reset(Clear));  // open: Qn, preset, en

  // Notes on the sheet:
  //   Caio Ragacci Pimentel - 405794
  //   Guia 11 - 01
endmodule

module Exercicio2 (
  input  Input,
  input  Clear,
  output [5:0] \saída 
);

  wire Clock_out;

  Clock Clock (.out(Clock_out));
  D_Flip_Flop d_ff_1 (.clk(Clock_out), .D(Input), .Q(\saída [5]), .reset(Clear));  // open: Qn, preset, en
  D_Flip_Flop d_ff_2 (.clk(Clock_out), .D(\saída [5]), .Q(\saída [4]), .reset(Clear));  // open: Qn, preset, en
  D_Flip_Flop d_ff_3 (.clk(Clock_out), .D(\saída [4]), .Q(\saída [3]), .reset(Clear));  // open: Qn, preset, en
  D_Flip_Flop d_ff_4 (.clk(Clock_out), .D(\saída [3]), .Q(\saída [2]), .reset(Clear));  // open: Qn, preset, en
  D_Flip_Flop d_ff_5 (.clk(Clock_out), .D(\saída [2]), .Q(\saída [1]), .reset(Clear));  // open: Qn, preset, en
  D_Flip_Flop d_ff_6 (.clk(Clock_out), .D(\saída [1]), .Q(\saída [0]), .reset(Clear));  // open: Qn, preset, en

  // Notes on the sheet:
  //   Caio Ragacci Pimentel - 405794
  //   Guia 11 - 02
endmodule

module Exercicio3 (
  input  Input,
  input  Clear,
  output [5:0] \saída 
);

  wire Clock_out;

  Clock Clock (.out(Clock_out));
  D_Flip_Flop d_ff_1 (.clk(Clock_out), .D(Input), .Q(\saída [5]), .reset(Clear));  // open: Qn, preset, en
  D_Flip_Flop d_ff_2 (.clk(Clock_out), .D(\saída [5]), .Q(\saída [4]), .reset(Clear));  // open: Qn, preset, en
  D_Flip_Flop d_ff_3 (.clk(Clock_out), .D(\saída [4]), .Q(\saída [3]), .reset(Clear));  // open: Qn, preset, en
  D_Flip_Flop d_ff_4 (.clk(Clock_out), .D(\saída [3]), .Q(\saída [2]), .reset(Clear));  // open: Qn, preset, en
  D_Flip_Flop d_ff_5 (.clk(Clock_out), .D(\saída [2]), .Q(\saída [1]), .reset(Clear));  // open: Qn, preset, en
  D_Flip_Flop d_ff_6 (.clk(Clock_out), .D(\saída [1]), .Q(\saída [0]), .reset(Clear));  // open: Qn, preset, en

  // Notes on the sheet:
  //   Caio Ragacci Pimentel - 405794
  //   Guia 11 - 03
endmodule

module Exercicio4 (
  input  Input,
  input  Clear,
  output [5:0] \saída 
);

  wire Clock_out;

  Clock Clock (.out(Clock_out));
  D_Flip_Flop d_ff_1 (.clk(Clock_out), .D(Input), .Q(\saída [5]), .reset(Clear));  // open: Qn, preset, en
  D_Flip_Flop d_ff_2 (.clk(Clock_out), .D(\saída [5]), .Q(\saída [4]), .reset(Clear));  // open: Qn, preset, en
  D_Flip_Flop d_ff_3 (.clk(Clock_out), .D(\saída [4]), .Q(\saída [3]), .reset(Clear));  // open: Qn, preset, en
  D_Flip_Flop d_ff_4 (.clk(Clock_out), .D(\saída [3]), .Q(\saída [2]), .reset(Clear));  // open: Qn, preset, en
  D_Flip_Flop d_ff_5 (.clk(Clock_out), .D(\saída [2]), .Q(\saída [1]), .reset(Clear));  // open: Qn, preset, en
  D_Flip_Flop d_ff_6 (.clk(Clock_out), .D(\saída [1]), .Q(\saída [0]), .reset(Clear));  // open: Qn, preset, en

  // Notes on the sheet:
  //   Caio Ragacci Pimentel - 405794
  //   Guia 11 - 04
endmodule

module Exercicio5 (
  input  Input,
  input  Clear,
  output [5:0] \saída 
);

  wire Clock_out;

  Clock Clock (.out(Clock_out));
  D_Flip_Flop d_ff_1 (.clk(Clock_out), .D(Input), .Q(\saída [5]), .reset(Clear));  // open: Qn, preset, en
  D_Flip_Flop d_ff_2 (.clk(Clock_out), .D(\saída [5]), .Q(\saída [4]), .reset(Clear));  // open: Qn, preset, en
  D_Flip_Flop d_ff_3 (.clk(Clock_out), .D(\saída [4]), .Q(\saída [3]), .reset(Clear));  // open: Qn, preset, en
  D_Flip_Flop d_ff_4 (.clk(Clock_out), .D(\saída [3]), .Q(\saída [2]), .reset(Clear));  // open: Qn, preset, en
  D_Flip_Flop d_ff_5 (.clk(Clock_out), .D(\saída [2]), .Q(\saída [1]), .reset(Clear));  // open: Qn, preset, en
  D_Flip_Flop d_ff_6 (.clk(Clock_out), .D(\saída [1]), .Q(\saída [0]), .reset(Clear));  // open: Qn, preset, en

  // Notes on the sheet:
  //   Caio Ragacci Pimentel - 405794
  //   Guia 11 - 05
endmodule
