// Logisim project guia 11.circ as structural Verilog: 5 circuits, main circuit Guia 11 -  exercicio01
module Guia_11____exercicio01 (
  input  Entrada,
  input  clear,
  output [5:0] out_3
);

  wire clock_1_out;

  Clock clock_1 (.out(clock_1_out));
  D_Flip_Flop d_ff_1 (.clk(clock_1_out), .D(Entrada), .Q(out_3[5]), .reset(clear));  // open: Qn, preset, en
  D_Flip_Flop d_ff_2 (.clk(clock_1_out), .D(out_3[5]), .Q(out_3[4]), .reset(clear));  // open: Qn, preset, en
  D_Flip_Flop d_ff_3 (.clk(clock_1_out), .D(out_3[4]), .Q(out_3[3]), .reset(clear));  // open: Qn, preset, en
  D_Flip_Flop d_ff_4 (.clk(clock_1_out), .D(out_3[3]), .Q(out_3[2]), .reset(clear));  // open: Qn, preset, en
  D_Flip_Flop d_ff_5 (.clk(clock_1_out), .D(out_3[2]), .Q(out_3[1]), .reset(clear));  // open: Qn, preset, en
  D_Flip_Flop #(.trigger("low")) d_ff_6 (
    .clk(clock_1_out), .D(out_3[1]), .Q(out_3[0]), .reset(clear));  // open: Qn, preset, en

  // Notes on the sheet:
  //   deslocamento de bits para esquerda
  //   Saida
endmodule

module Guia_11___exercicio_02 (
  input  in_1,
  input  in_2,
  input  in_3,
  input  [1:0] in_4
);

  wire and_1_out, and_2_out, clock_1_out, j_k_ff_1_q, j_k_ff_1_qn, not_1_out;

  Clock clock_1 (.out(clock_1_out));
  not not_1 (not_1_out, in_1);
  J_K_Flip_Flop j_k_ff_1 (
    .J(in_1), .clk(clock_1_out), .K(not_1_out), .Q(j_k_ff_1_q), .Qn(j_k_ff_1_qn), .preset(and_1_out),
    .reset(in_2));  // open: en
  and and_1 (and_1_out, in_4[1], in_3);
  J_K_Flip_Flop j_k_ff_2 (
    .J(j_k_ff_1_q), .clk(clock_1_out), .K(j_k_ff_1_qn), .preset(and_2_out), .reset(in_2));  // open: Q, Qn, en
  and and_2 (and_2_out, in_3, in_4[0]);
endmodule

module Guia_11___exercicio03 (
  input  in_1
);

  wire clock_1_out, j_k_ff_2_q, j_k_ff_3_q, j_k_ff_4_q, j_k_ff_5_q;

  J_K_Flip_Flop j_k_ff_1 (.J(1'b1), .clk(j_k_ff_2_q), .K(1'b1), .reset(in_1));  // open: Q, Qn, preset, en
  J_K_Flip_Flop j_k_ff_2 (.J(1'b1), .clk(j_k_ff_3_q), .K(1'b1), .Q(j_k_ff_2_q), .reset(in_1));  // open: Qn, preset, en
  J_K_Flip_Flop j_k_ff_3 (.J(1'b1), .clk(j_k_ff_4_q), .K(1'b1), .Q(j_k_ff_3_q), .reset(in_1));  // open: Qn, preset, en
  J_K_Flip_Flop j_k_ff_4 (.J(1'b1), .clk(j_k_ff_5_q), .K(1'b1), .Q(j_k_ff_4_q), .reset(in_1));  // open: Qn, preset, en
  J_K_Flip_Flop j_k_ff_5 (.J(1'b1), .clk(clock_1_out), .K(1'b1), .Q(j_k_ff_5_q), .reset(in_1));  // open: Qn, preset, en
  Clock clock_1 (.out(clock_1_out));
endmodule

module GUIA_11___exercicio04 (
  input  in_1,
  input  in_2,
  output [4:0] out_3
);

  wire clock_1_out;

  Clock clock_1 (.out(clock_1_out));
  D_Flip_Flop d_ff_1 (.clk(clock_1_out), .D(in_1), .Q(out_3[4]), .reset(in_2));  // open: Qn, preset, en
  D_Flip_Flop d_ff_2 (.clk(clock_1_out), .D(out_3[4]), .Q(out_3[3]), .reset(in_2));  // open: Qn, preset, en
  D_Flip_Flop d_ff_3 (.clk(clock_1_out), .D(out_3[3]), .Q(out_3[2]));  // open: Qn, preset, en, reset
  D_Flip_Flop d_ff_4 (.clk(clock_1_out), .D(out_3[2]), .Q(out_3[1]), .reset(in_2));  // open: Qn, preset, en
  D_Flip_Flop d_ff_5 (.clk(clock_1_out), .D(out_3[1]), .Q(out_3[0]), .reset(in_2));  // open: Qn, preset, en
endmodule

module Guia_11____exercicio05 (
  input  in_1
);

  wire clock_1_out, j_k_ff_2_qn, j_k_ff_3_qn, j_k_ff_4_qn, j_k_ff_5_qn;

  J_K_Flip_Flop j_k_ff_1 (
    .J(j_k_ff_3_qn), .clk(j_k_ff_2_qn), .K(j_k_ff_3_qn), .reset(in_1));  // open: Q, Qn, preset, en
  J_K_Flip_Flop j_k_ff_2 (
    .J(j_k_ff_3_qn), .clk(j_k_ff_3_qn), .K(j_k_ff_3_qn), .Qn(j_k_ff_2_qn), .reset(in_1));  // open: Q, preset, en
  J_K_Flip_Flop j_k_ff_3 (
    .J(j_k_ff_3_qn), .clk(j_k_ff_4_qn), .K(j_k_ff_3_qn), .Qn(j_k_ff_3_qn), .reset(in_1));  // open: Q, preset, en
  J_K_Flip_Flop j_k_ff_4 (
    .J(j_k_ff_3_qn), .clk(j_k_ff_5_qn), .K(j_k_ff_3_qn), .Qn(j_k_ff_4_qn), .reset(in_1));  // open: Q, preset, en
  Clock clock_1 (.out(clock_1_out));
  J_K_Flip_Flop j_k_ff_5 (
    .J(j_k_ff_3_qn), .clk(clock_1_out), .K(j_k_ff_3_qn), .Qn(j_k_ff_5_qn), .reset(in_1));  // open: Q, preset, en
  // also tied to VCC on the sheet: j_k_ff_3_qn
endmodule
