// Logisim project exer1.circ as structural Verilog: 1 circuit, main circuit Exer1
module Exer1 (
  input  Input,
  input  clear,
  output out_3,
  output out_4,
  output out_5,
  output out_6,
  output out_7,
  output out_8
);

  wire Clock_out;

  Clock Clock (.out(Clock_out));
  D_Flip_Flop d_ff_1 (.clk(Clock_out), .D(out_4), .Q(out_3), .preset(clear));  // open: Qn, en, reset
  D_Flip_Flop d_ff_2 (.clk(Clock_out), .D(out_5), .Q(out_4), .reset(clear));  // open: Qn, preset, en
  D_Flip_Flop d_ff_3 (.clk(Clock_out), .D(out_6), .Q(out_5), .reset(clear));  // open: Qn, preset, en
  D_Flip_Flop d_ff_4 (.clk(Clock_out), .D(out_7), .Q(out_6), .reset(clear));  // open: Qn, preset, en
  D_Flip_Flop d_ff_5 (.clk(Clock_out), .D(out_8), .Q(out_7), .reset(clear));  // open: Qn, preset, en
  D_Flip_Flop d_ff_6 (.clk(Clock_out), .D(Input), .Q(out_8), .reset(clear));  // open: Qn, preset, en

  // Notes on the sheet:
  //   Marley Ribeiro - 414510
endmodule
