// Logisim project guia_12.circ as structural Verilog: 9 circuits, main circuit reg JK
module guia12_ex01 (
  input  [3:0] In,
  input  R_W,
  input  CLK,
  input  CS,
  input  CLR,
  output [3:0] Out
);

  wire and_1_out, and_2_out, not_1_out, not_2_out, not_3_out;
  wire [3:0] controlled_buffer_1_out, reg_jk_1_out;

  not not_1 (not_1_out, R_W);
  and and_1 (and_1_out, not_1_out, not_2_out);
  not not_2 (not_2_out, CS);
  not not_3 (not_3_out, CS);
  assign controlled_buffer_1_out = and_1_out ? In : 4'bz;  // Controlled_Buffer controlled_buffer_1
  reg_JK reg_jk_1 (.E(controlled_buffer_1_out), .CLK(CLK), .CLR(CLR), .out(reg_jk_1_out));
  and and_2 (and_2_out, not_3_out, R_W);
  assign Out = and_2_out ? reg_jk_1_out : 4'bz;  // Controlled_Buffer controlled_buffer_2

  // Notes on the sheet:
  //   Anderson Belchior de Carvalho - 396673
endmodule

module guia12_ex02 (
  input  [7:0] In,
  input  R_W,
  input  CS,
  input  CLK,
  input  CLR,
  output [7:0] Out
);

  // guia12_ex01 guia12_ex01_1: pin names not known; wires that end beside it: R_W, CLK, CS, CLR, In[7:4], Out[7:4]
  // guia12_ex01 guia12_ex01_2: pin names not known; wires that end beside it: R_W, CLK, CS, CLR, In[3:0], Out[3:0]

  // Notes on the sheet:
  //   Anderson Belchior de Carvalho - 396673
endmodule

module guia12_ex03 (
  input  R_W,
  input  [7:0] In,
  input  [1:0] adress,
  input  CLR,
  output [7:0] Out
);

  wire clock_1_out, decoder_1_out0, decoder_1_out1, decoder_1_out2, decoder_1_out3, not_1_out, not_2_out,
       not_3_out, not_4_out;

  Clock clock_1 (.out(clock_1_out));
  Decoder #(.select(2)) decoder_1 (
    .out0(decoder_1_out0), .out1(decoder_1_out1), .out2(decoder_1_out2), .out3(decoder_1_out3), .sel(adress));
  not not_1 (not_1_out, decoder_1_out0);
  not not_2 (not_2_out, decoder_1_out1);
  not not_3 (not_3_out, decoder_1_out2);
  not not_4 (not_4_out, decoder_1_out3);
  // guia12_ex02 guia12_ex02_1: pin names not known; wires that end beside it: R_W, not_1_out, clock_1_out, CLR, In, Out, In
  // guia12_ex02 guia12_ex02_2: pin names not known; wires that end beside it: R_W, not_2_out, clock_1_out, CLR, In, Out, In
  // guia12_ex02 guia12_ex02_3: pin names not known; wires that end beside it: R_W, not_3_out, clock_1_out, CLR, In, Out, In
  // guia12_ex02 guia12_ex02_4: pin names not known; wires that end beside it: R_W, not_4_out, clock_1_out, CLR, In, Out

  // Notes on the sheet:
  //   Anderson Belchior de Carvalho - 396673
endmodule

module guia12_ex04 (
  input  R_W,
  input  [3:0] In,
  input  adress,
  input  CLR,
  output [3:0] Out
);

  wire CLK_out, decoder_1_out0, decoder_1_out1, not_1_out, not_2_out;

  Clock CLK (.out(CLK_out));
  not not_1 (not_1_out, decoder_1_out0);
  not not_2 (not_2_out, decoder_1_out1);
  Decoder decoder_1 (.out0(decoder_1_out0), .out1(decoder_1_out1), .sel(adress));
  RAM1x4D ram1x4d_1 (.R_W(R_W), .CLK(CLK_out), .CS(not_1_out), .CLR(CLR), .In(In), .Out(Out));
  RAM1x4D ram1x4d_2 (.R_W(R_W), .CLK(CLK_out), .CS(not_2_out), .CLR(CLR), .In(In), .Out(Out));

  // Notes on the sheet:
  //   Anderson Belchior de Carvalho - 396673
endmodule

module guia12_ex05 (
  input  R_W,
  input  [7:0] In,
  input  [1:0] adress,
  input  CLR,
  output [7:0] Out
);

  wire clock_1_out, decoder_1_out0, decoder_1_out1, decoder_1_out2, decoder_1_out3, not_1_out, not_2_out,
       not_3_out, not_4_out;

  Clock clock_1 (.out(clock_1_out));
  not not_1 (not_1_out, decoder_1_out0);
  not not_2 (not_2_out, decoder_1_out1);
  not not_3 (not_3_out, decoder_1_out2);
  not not_4 (not_4_out, decoder_1_out3);
  Decoder #(.select(2)) decoder_1 (
    .out0(decoder_1_out0), .out1(decoder_1_out1), .out2(decoder_1_out2), .out3(decoder_1_out3), .sel(adress));
  RAM1x8D ram1x8d_1 (.R_W(R_W), .CS(not_1_out), .CLK(clock_1_out), .CLR(CLR), .In(In), .Out(Out));
  RAM1x8D ram1x8d_2 (.R_W(R_W), .CS(not_2_out), .CLK(clock_1_out), .CLR(CLR), .In(In), .Out(Out));
  RAM1x8D ram1x8d_3 (.R_W(R_W), .CS(not_3_out), .CLK(clock_1_out), .CLR(CLR), .In(In), .Out(Out));
  RAM1x8D ram1x8d_4 (.R_W(R_W), .CS(not_4_out), .CLK(clock_1_out), .CLR(CLR), .In(In), .Out(Out));

  // Notes on the sheet:
  //   Anderson Belchior de Carvalho - 396673
endmodule

module reg_JK (
  input  [3:0] E,
  input  CLK,
  input  CLR,
  output [3:0] out
);

  wire not_1_out, not_2_out, not_3_out, not_4_out;

  J_K_Flip_Flop j_k_ff_1 (.J(E[3]), .clk(CLK), .K(not_1_out), .Q(out[3]), .reset(CLR));  // open: Qn, preset, en
  not not_1 (not_1_out, E[3]);
  not not_2 (not_2_out, E[2]);
  J_K_Flip_Flop j_k_ff_2 (.J(E[2]), .clk(CLK), .K(not_2_out), .Q(out[2]), .reset(CLR));  // open: Qn, preset, en
  not not_3 (not_3_out, E[1]);
  J_K_Flip_Flop j_k_ff_3 (.J(E[1]), .clk(CLK), .K(not_3_out), .Q(out[1]), .reset(CLR));  // open: Qn, preset, en
  not not_4 (not_4_out, E[0]);
  J_K_Flip_Flop j_k_ff_4 (.J(E[0]), .clk(CLK), .K(not_4_out), .Q(out[0]), .reset(CLR));  // open: Qn, preset, en

  // Notes on the sheet:
  //   Anderson Belchior de Carvalho - 396673
endmodule

module reg_D (
  input  [3:0] In,
  input  CLK,
  input  CLR,
  output [3:0] Out
);

  D_Flip_Flop d_ff_1 (.clk(CLK), .D(In[3]), .Q(Out[3]), .reset(CLR));  // open: Qn, preset, en
  D_Flip_Flop d_ff_2 (.clk(CLK), .D(In[2]), .Q(Out[2]), .reset(CLR));  // open: Qn, preset, en
  D_Flip_Flop d_ff_3 (.clk(CLK), .D(In[1]), .Q(Out[1]), .reset(CLR));  // open: Qn, preset, en
  D_Flip_Flop d_ff_4 (.clk(CLK), .D(In[0]), .Q(Out[0]), .reset(CLR));  // open: Qn, preset, en

  // Notes on the sheet:
  //   Anderson Belchior de Carvalho - 396673
endmodule

module RAM1x4D (
  input  [3:0] In,
  input  R_W,
  input  CLK,
  input  CS,
  input  CLR,
  output [3:0] Out
);

  wire and_1_out, and_2_out, not_1_out, not_2_out, not_3_out;
  wire [3:0] controlled_buffer_1_out, reg_d_1_out;

  not not_1 (not_1_out, R_W);
  not not_2 (not_2_out, CS);
  not not_3 (not_3_out, CS);
  and and_1 (and_1_out, not_1_out, not_2_out);
  assign controlled_buffer_1_out = and_1_out ? In : 4'bz;  // Controlled_Buffer controlled_buffer_1
  and and_2 (and_2_out, not_3_out, R_W);
  reg_D reg_d_1 (.In(controlled_buffer_1_out), .CLK(CLK), .CLR(CLR), .Out(reg_d_1_out));
  assign Out = and_2_out ? reg_d_1_out : 4'bz;  // Controlled_Buffer controlled_buffer_2

  // Notes on the sheet:
  //   Anderson Belchior de Carvalho - 396673
endmodule

module RAM1x8D (
  input  [7:0] In,
  input  R_W,
  input  CS,
  input  CLK,
  input  CLR,
  output [7:0] Out
);

  RAM1x4D ram1x4d_1 (.R_W(R_W), .CLK(CLK), .CS(CS), .CLR(CLR), .In(In[7:4]), .Out(Out[7:4]));
  RAM1x4D ram1x4d_2 (.R_W(R_W), .CLK(CLK), .CS(CS), .CLR(CLR), .In(In[3:0]), .Out(Out[3:0]));

  // Notes on the sheet:
  //   Anderson Belchior de Carvalho - 396673
endmodule
