// Logisim project Guia_12.circ as structural Verilog
module JK (
  input  [3:0] IMPUT,
  input  CLCK,
  input  CLR,
  output [3:0] OUPUT
);

  wire not_1_out, not_2_out, not_3_out, not_4_out;

  J_K_Flip_Flop j_k_ff_1 (.J(IMPUT[3]), .clk(CLCK), .K(not_1_out), .Q(OUPUT[0]), .preset(CLR));  // open: Qn, en, reset
  not not_1 (not_1_out, IMPUT[3]);
  J_K_Flip_Flop j_k_ff_2 (.J(IMPUT[2]), .clk(CLCK), .K(not_2_out), .Q(OUPUT[1]), .preset(CLR));  // open: Qn, en, reset
  not not_2 (not_2_out, IMPUT[2]);
  J_K_Flip_Flop j_k_ff_3 (.J(IMPUT[1]), .clk(CLCK), .K(not_3_out), .Q(OUPUT[2]), .preset(CLR));  // open: Qn, en, reset
  not not_3 (not_3_out, IMPUT[1]);
  not not_4 (not_4_out, IMPUT[0]);
  J_K_Flip_Flop j_k_ff_4 (.J(IMPUT[0]), .clk(CLCK), .K(not_4_out), .Q(OUPUT[3]), .preset(CLR));  // open: Qn, en, reset

  // Notes on the sheet:
  //   Karen Alves Pereira - 407451
endmodule

module D (
  input  [3:0] IMPUT,
  input  CLCK,
  input  CLR,
  output [3:0] OUPUT
);

  D_Flip_Flop d_ff_1 (.clk(CLCK), .D(IMPUT[3]), .Q(OUPUT[0]), .preset(CLR));  // open: Qn, en, reset
  D_Flip_Flop d_ff_2 (.clk(CLCK), .D(IMPUT[2]), .Q(OUPUT[1]), .preset(CLR));  // open: Qn, en, reset
  D_Flip_Flop d_ff_3 (.clk(CLCK), .D(IMPUT[1]), .Q(OUPUT[2]), .preset(CLR));  // open: Qn, en, reset
  D_Flip_Flop d_ff_4 (.clk(CLCK), .D(IMPUT[0]), .Q(OUPUT[3]), .preset(CLR));  // open: Qn, en, reset

  // Notes on the sheet:
  //   Karen Alves Pereira - 407451
endmodule

// 1-4D
module RAM1_4D (
  input  [3:0] IMPUT,
  input  RW,
  input  CLCK,
  input  CS,
  input  CLR,
  output [3:0] OUTPUT
);

  wire and_1_out, and_2_out, not_1_out, not_2_out, not_3_out;
  wire [3:0] controlled_buffer_1_out, d_1_ouput;

  not not_1 (not_1_out, RW);
  not not_2 (not_2_out, CS);
  not not_3 (not_3_out, CS);
  and and_1 (and_1_out, not_1_out, not_2_out);
  and and_2 (and_2_out, not_3_out, RW);
  assign controlled_buffer_1_out = and_1_out ? IMPUT : 4'bz;  // Controlled_Buffer controlled_buffer_1
  D d_1 (.IMPUT(controlled_buffer_1_out), .CLCK(CLR), .CLR(CLCK), .OUPUT(d_1_ouput));
  assign OUTPUT = and_2_out ? d_1_ouput : 4'bz;  // Controlled_Buffer controlled_buffer_2

  // Notes on the sheet:
  //   Karen Alves Pereira - 407451
endmodule

// 1-8D
module RAM1_8D (
  input  [7:0] IMPUT,
  input  RW,
  input  CS,
  input  CLCK,
  input  CLR,
  output [7:0] OUTPUT
);

  RAM1_4D ram1_4d_1 (.RW(RW), .CLCK(CS), .CS(CLCK), .CLR(CLR), .IMPUT(IMPUT[7:4]), .OUTPUT(OUTPUT[3:0]));
  RAM1_4D ram1_4d_2 (.RW(RW), .CLCK(CS), .CS(CLCK), .CLR(CLR), .IMPUT(IMPUT[3:0]), .OUTPUT(OUTPUT[7:4]));

  // Notes on the sheet:
  //   Karen Alces Pereira - 407451
endmodule

module ex01 (
  input  [3:0] IMPUT,
  input  RW,
  input  CLCK,
  input  CLR,
  input  CS,
  output [3:0] OUPUT
);

  wire and_1_out, and_2_out, not_1_out, not_2_out, not_3_out;
  wire [3:0] controlled_buffer_1_out, jk_1_ouput;

  not not_1 (not_1_out, RW);
  not not_2 (not_2_out, CS);
  not not_3 (not_3_out, CS);
  and and_1 (and_1_out, not_1_out, not_2_out);
  assign controlled_buffer_1_out = and_1_out ? IMPUT : 4'bz;  // Controlled_Buffer controlled_buffer_1
  and and_2 (and_2_out, not_3_out, RW);
  JK jk_1 (.IMPUT(controlled_buffer_1_out), .CLCK(CLCK), .CLR(CLR), .OUPUT(jk_1_ouput));
  assign OUPUT = and_2_out ? jk_1_ouput : 4'bz;  // Controlled_Buffer controlled_buffer_2

  // Notes on the sheet:
  //   Karen Alves Pereira - 407451
  //   INPUT
endmodule

module ex02 (
  input  [7:0] IMPUT,
  input  RW,
  input  CS,
  input  CLCK,
  input  CLR,
  output [7:0] OUPUT
);

  RAM1_4D ram1_4d_1 (.RW(RW), .CLCK(CS), .CS(CLCK), .CLR(CLR), .IMPUT(IMPUT[7:4]), .OUTPUT(OUPUT[7:4]));
  RAM1_4D ram1_4d_2 (.RW(RW), .CLCK(CS), .CS(CLCK), .CLR(CLR), .IMPUT(IMPUT[3:0]), .OUTPUT(OUPUT[3:0]));

  // Notes on the sheet:
  //   Karen Alves Pereira - 407451
endmodule

module ex03 (
  input  [7:0] IMPUT,
  input  CLR,
  input  RW,
  input  [1:0] ADDSS,
  output [7:0] OTPUT
);

  wire clock_1_out, decoder_1_out0, decoder_1_out1, decoder_1_out2, decoder_1_out3, not_1_out, not_2_out,
       not_3_out, not_4_out;

  Clock clock_1 (.out(clock_1_out));
  Decoder #(.select(2), .enable("false")) decoder_1 (
    .out0(decoder_1_out0), .out1(decoder_1_out1), .out2(decoder_1_out2), .out3(decoder_1_out3), .sel(ADDSS));
  not not_1 (not_1_out, decoder_1_out0);
  not not_2 (not_2_out, decoder_1_out1);
  not not_3 (not_3_out, decoder_1_out2);
  not not_4 (not_4_out, decoder_1_out3);
  RAM1_8D ram1_8d_1 (.IMPUT(IMPUT), .RW(CLR), .CS(RW), .CLCK(clock_1_out), .CLR(not_1_out), .OUTPUT(OTPUT));
  RAM1_8D ram1_8d_2 (.IMPUT(IMPUT), .RW(CLR), .CS(RW), .CLCK(clock_1_out), .CLR(not_2_out), .OUTPUT(OTPUT));
  RAM1_8D ram1_8d_3 (.IMPUT(IMPUT), .RW(CLR), .CS(RW), .CLCK(clock_1_out), .CLR(not_3_out), .OUTPUT(OTPUT));
  RAM1_8D ram1_8d_4 (.IMPUT(IMPUT), .RW(CLR), .CS(RW), .CLCK(clock_1_out), .CLR(not_4_out), .OUTPUT(OTPUT));

  // Notes on the sheet:
  //   Karen Alves Pereira - 407451
endmodule

module ex04 (
  input  [3:0] IMPUT,
  input  RW,
  input  CLR,
  input  ADSS,
  output [3:0] OUTPUT
);

  wire clock_1_out, decoder_1_out0, decoder_1_out1, not_1_out, not_2_out;

  Clock clock_1 (.out(clock_1_out));
  Decoder #(.enable("false")) decoder_1 (.out0(decoder_1_out0), .out1(decoder_1_out1), .sel(ADSS));
  not not_1 (not_1_out, decoder_1_out0);
  not not_2 (not_2_out, decoder_1_out1);
  RAM1_4D ram1_4d_1 (.RW(RW), .CLCK(clock_1_out), .CS(CLR), .CLR(not_1_out), .IMPUT(IMPUT), .OUTPUT(OUTPUT));
  RAM1_4D ram1_4d_2 (.RW(RW), .CLCK(clock_1_out), .CS(CLR), .CLR(not_2_out), .IMPUT(IMPUT), .OUTPUT(OUTPUT));

  // Notes on the sheet:
  //   Karen Alves Pereira - 407451
endmodule

module ex05 (
  input  [7:0] IMPUT,
  input  CLR,
  input  RW,
  input  [1:0] ADDSS,
  output [7:0] OTPUT
);

  wire clock_1_out, decoder_1_out0, decoder_1_out1, decoder_1_out2, decoder_1_out3, not_1_out, not_2_out,
       not_3_out, not_4_out;

  Clock clock_1 (.out(clock_1_out));
  Decoder #(.select(2), .enable("false")) decoder_1 (
    .out0(decoder_1_out0), .out1(decoder_1_out1), .out2(decoder_1_out2), .out3(decoder_1_out3), .sel(ADDSS));
  not not_1 (not_1_out, decoder_1_out0);
  not not_2 (not_2_out, decoder_1_out1);
  not not_3 (not_3_out, decoder_1_out2);
  not not_4 (not_4_out, decoder_1_out3);
  RAM1_8D ram1_8d_1 (.IMPUT(IMPUT), .RW(CLR), .CS(RW), .CLCK(clock_1_out), .CLR(not_1_out), .OUTPUT(OTPUT));
  RAM1_8D ram1_8d_2 (.IMPUT(IMPUT), .RW(CLR), .CS(RW), .CLCK(clock_1_out), .CLR(not_2_out), .OUTPUT(OTPUT));
  RAM1_8D ram1_8d_3 (.IMPUT(IMPUT), .RW(CLR), .CS(RW), .CLCK(clock_1_out), .CLR(not_3_out), .OUTPUT(OTPUT));
  RAM1_8D ram1_8d_4 (.IMPUT(IMPUT), .RW(CLR), .CS(RW), .CLCK(clock_1_out), .CLR(not_4_out), .OUTPUT(OTPUT));

  // Notes on the sheet:
  //   Karen Alves Pereira - 407451
endmodule
