// Logisim project Guia 12.circ as structural Verilog: 3 circuits, main circuit RAM_1x4
module RAM_1x4 (
  input  CLOCK,
  input  R_W,
  input  ADRESS,
  input  [3:0] INPUT,
  input  CLR,
  output [3:0] OUTPUT
);

  wire and_1_out;
  wire [3:0] j_k_ff_1_q;

  and and_1 (and_1_out, CLOCK, R_W, ADRESS);
  J_K_Flip_Flop j_k_ff_1 (
    .J(INPUT[0]), .clk(and_1_out), .K(INPUT[0]), .Q(j_k_ff_1_q[0]), .reset(CLR));  // open: Qn, preset, en
  J_K_Flip_Flop j_k_ff_2 (
    .J(INPUT[1]), .clk(and_1_out), .K(INPUT[1]), .Q(j_k_ff_1_q[1]), .reset(CLR));  // open: Qn, preset, en
  J_K_Flip_Flop j_k_ff_3 (
    .J(INPUT[2]), .clk(and_1_out), .K(INPUT[2]), .Q(j_k_ff_1_q[2]), .reset(CLR));  // open: Qn, preset, en
  J_K_Flip_Flop j_k_ff_4 (
    .J(INPUT[3]), .clk(and_1_out), .K(INPUT[3]), .Q(j_k_ff_1_q[3]), .reset(CLR));  // open: Qn, preset, en
  assign OUTPUT = ADRESS ? j_k_ff_1_q : 4'bz;  // Controlled_Buffer controlled_buffer_1

  // Notes on the sheet:
  //   Bruno César Lopes Silva - 415985
endmodule

module RAM_1x8 (
  input  CLOCK,
  input  R_W,
  input  ADRESS,
  input  [7:0] INPUT,
  input  CLEAR,
  output [7:0] OUTPUT
);

  RAM_1x4 ram_1x4_1 (.CLOCK(CLOCK), .R_W(R_W), .ADRESS(ADRESS), .INPUT(INPUT[3:0]), .CLR(CLEAR), .OUTPUT(OUTPUT[3:0]));
  RAM_1x4 ram_1x4_2 (.CLOCK(CLOCK), .R_W(R_W), .ADRESS(ADRESS), .INPUT(INPUT[7:4]), .CLR(CLEAR), .OUTPUT(OUTPUT[7:4]));

  // Notes on the sheet:
  //   Bruno César Lopes Silva - 415985
endmodule

module RAM_4x8 (
  input  CLOCK,
  input  R_W,
  input  [1:0] ADRESS,
  input  [7:0] INPUT,
  input  CLEAR,
  output [7:0] OUTPUT
);

  wire demultiplexer_1_out0, demultiplexer_1_out1, demultiplexer_1_out2, demultiplexer_1_out3;
  wire [7:0] ram_1x8_1_output, ram_1x8_2_output, ram_1x8_3_output, ram_1x8_4_output;

  Demultiplexer #(.select(2), .enable("false")) demultiplexer_1 (
    .out0(demultiplexer_1_out0), .out1(demultiplexer_1_out1), .out2(demultiplexer_1_out2),
    .out3(demultiplexer_1_out3), .in(CLOCK), .sel(ADRESS));
  RAM_1x8 ram_1x8_1 (
    .CLOCK(CLOCK), .R_W(R_W), .ADRESS(demultiplexer_1_out0), .INPUT(INPUT), .CLEAR(CLEAR),
    .OUTPUT(ram_1x8_1_output));
  RAM_1x8 ram_1x8_2 (
    .CLOCK(CLOCK), .R_W(R_W), .ADRESS(demultiplexer_1_out1), .INPUT(INPUT), .CLEAR(CLEAR),
    .OUTPUT(ram_1x8_2_output));
  RAM_1x8 ram_1x8_3 (
    .CLOCK(CLOCK), .R_W(R_W), .ADRESS(demultiplexer_1_out2), .INPUT(INPUT), .CLEAR(CLEAR),
    .OUTPUT(ram_1x8_3_output));
  RAM_1x8 ram_1x8_4 (
    .CLOCK(CLOCK), .R_W(R_W), .ADRESS(demultiplexer_1_out3), .INPUT(INPUT), .CLEAR(CLEAR),
    .OUTPUT(ram_1x8_4_output));
  Multiplexer #(.select(2), .width(8), .enable("false")) multiplexer_1 (
    .in0(ram_1x8_1_output), .in1(ram_1x8_2_output), .in2(ram_1x8_3_output), .in3(ram_1x8_4_output),
    .out(OUTPUT), .sel(ADRESS));

  // Notes on the sheet:
  //   Bruno César Lopes Silva - 415985
endmodule
