// Logisim project Guia12.circ as structural Verilog: 4 circuits, main circuit Registrador 4 Bits
// REG4
module Registrador_4_Bits (
  input  CLK,
  input  [3:0] \input ,
  input  CLR,
  output [3:0] \output 
);

  wire not_1_out, not_2_out, not_3_out, not_4_out;

  J_K_Flip_Flop j_k_ff_1 (
    .J(\input [0]), .clk(CLK), .K(not_1_out), .Q(\output [0]), .reset(CLR));  // open: Qn, preset, en
  not not_1 (not_1_out, \input [0]);
  J_K_Flip_Flop j_k_ff_2 (
    .J(\input [1]), .clk(CLK), .K(not_2_out), .Q(\output [1]), .reset(CLR));  // open: Qn, preset, en
  not not_2 (not_2_out, \input [1]);
  J_K_Flip_Flop j_k_ff_3 (
    .J(\input [2]), .clk(CLK), .K(not_3_out), .Q(\output [2]), .reset(CLR));  // open: Qn, preset, en
  not not_3 (not_3_out, \input [2]);
  J_K_Flip_Flop j_k_ff_4 (
    .J(\input [3]), .clk(CLK), .K(not_4_out), .Q(\output [3]), .reset(CLR));  // open: Qn, preset, en
  not not_4 (not_4_out, \input [3]);

  // Notes on the sheet:
  //   Douglas Borges
endmodule

// RAM1x4
module Exercicio01___RAM_1x4 (
  input  [3:0] \input ,
  input  CLK,
  input  R___W,
  input  CLR,
  output [3:0] \output 
);

  wire not_1_out;
  wire [3:0] controlled_buffer_1_out, registrador_4_bits_1_output;

  assign controlled_buffer_1_out = R___W ? \input  : 4'bz;  // Controlled_Buffer controlled_buffer_1
  Registrador_4_Bits registrador_4_bits_1 (
    .\output (registrador_4_bits_1_output), .\input (controlled_buffer_1_out), .CLR(CLR), .CLK(CLK));
  not not_1 (not_1_out, R___W);
  assign \output  = not_1_out ? registrador_4_bits_1_output : 4'bz;  // Controlled_Buffer controlled_buffer_2

  // Notes on the sheet:
  //   Douglas Borges - 417889
endmodule

// RAM 1x8
module Exercicio02___RAM_1x8 (
  input  [7:0] Input,
  input  CLK,
  input  R___W,
  input  CLR,
  output [7:0] \output 
);

  Exercicio01___RAM_1x4 exercicio01_ram_1x4_1 (
    .\input (Input[7:4]), .CLK(CLK), .R___W(R___W), .CLR(CLR), .\output (\output [7:4]));
  Exercicio01___RAM_1x4 exercicio01_ram_1x4_2 (
    .\input (Input[3:0]), .CLK(CLK), .R___W(R___W), .CLR(CLR), .\output (\output [3:0]));

  // Notes on the sheet:
  //   Douglas Borges - 417889
endmodule

module Exercicio03___RAM_4x8 (
  input  [7:0] Input,
  input  [1:0] ADDR,
  input  R___W,
  input  in_4,
  output [7:0] \output 
);

  wire clock_1_out, not_1_out;
  wire [7:0] demultiplexer_1_out0, demultiplexer_1_out1, demultiplexer_1_out2, demultiplexer_1_out3,
       exercicio02_ram_1x8_1_output, exercicio02_ram_1x8_2_output, exercicio02_ram_1x8_3_output,
       exercicio02_ram_1x8_4_output;

  Demultiplexer #(.select(2), .width(8)) demultiplexer_1 (
    .out0(demultiplexer_1_out0), .out1(demultiplexer_1_out1), .out2(demultiplexer_1_out2),
    .out3(demultiplexer_1_out3), .in(Input), .sel(ADDR), .en(R___W));
  Clock clock_1 (.out(clock_1_out));
  Exercicio02___RAM_1x8 exercicio02_ram_1x8_1 (
    .CLK(clock_1_out), .R___W(R___W), .\output (exercicio02_ram_1x8_1_output), .Input(demultiplexer_1_out0),
    .CLR(in_4));
  Exercicio02___RAM_1x8 exercicio02_ram_1x8_2 (
    .CLK(clock_1_out), .R___W(R___W), .\output (exercicio02_ram_1x8_2_output), .Input(demultiplexer_1_out1),
    .CLR(in_4));
  Exercicio02___RAM_1x8 exercicio02_ram_1x8_3 (
    .CLK(clock_1_out), .R___W(R___W), .\output (exercicio02_ram_1x8_3_output), .Input(demultiplexer_1_out2),
    .CLR(in_4));
  Exercicio02___RAM_1x8 exercicio02_ram_1x8_4 (
    .CLK(clock_1_out), .R___W(R___W), .\output (exercicio02_ram_1x8_4_output), .Input(demultiplexer_1_out3),
    .CLR(in_4));
  Multiplexer #(.select(2), .width(8)) multiplexer_1 (
    .in0(exercicio02_ram_1x8_1_output), .in1(exercicio02_ram_1x8_2_output),
    .in2(exercicio02_ram_1x8_3_output), .in3(exercicio02_ram_1x8_4_output), .out(\output ), .sel(ADDR),
    .en(not_1_out));
  not not_1 (not_1_out, R___W);

  // Notes on the sheet:
  //   Douglas Borges - 417889
endmodule
