// Logisim project guia12.circ as structural Verilog: 9 circuits, main circuit reg JK
module reg_JK (
  input  [3:0] \input ,
  input  clock,
  input  clear,
  output [3:0] \output 
);

  wire not_1_out, not_2_out, not_3_out, not_4_out;

  J_K_Flip_Flop j_k_ff_1 (
    .J(\input [3]), .clk(clock), .K(not_1_out), .Q(\output [3]), .reset(clear));  // open: Qn, preset, en
  not not_1 (not_1_out, \input [3]);
  J_K_Flip_Flop j_k_ff_2 (
    .J(\input [2]), .clk(clock), .K(not_2_out), .Q(\output [2]), .reset(clear));  // open: Qn, preset, en
  not not_2 (not_2_out, \input [2]);
  J_K_Flip_Flop j_k_ff_3 (
    .J(\input [1]), .clk(clock), .K(not_3_out), .Q(\output [1]), .reset(clear));  // open: Qn, preset, en
  not not_3 (not_3_out, \input [1]);
  J_K_Flip_Flop j_k_ff_4 (
    .J(\input [0]), .clk(clock), .K(not_4_out), .Q(\output [0]), .reset(clear));  // open: Qn, preset, en
  not not_4 (not_4_out, \input [0]);

  // Notes on the sheet:
  //   Isabella Gonçales - 420120
endmodule

module Exercicio01 (
  input  [3:0] \input ,
  input  R_W,
  input  clock,
  input  CS,
  input  CLR,
  output [3:0] \output 
);

  wire and_1_out, and_2_out, not_1_out, not_2_out, not_3_out;
  wire [3:0] controlled_buffer_1_out, reg_jk_1_output;

  not not_1 (not_1_out, R_W);
  not not_2 (not_2_out, CS);
  not not_3 (not_3_out, CS);
  and and_1 (and_1_out, not_1_out, not_2_out);
  assign controlled_buffer_1_out = and_1_out ? \input  : 4'bz;  // Controlled_Buffer controlled_buffer_1
  and and_2 (and_2_out, not_3_out, R_W);
  reg_JK reg_jk_1 (.\input (controlled_buffer_1_out), .clock(clock), .clear(CLR), .\output (reg_jk_1_output));
  assign \output  = and_2_out ? reg_jk_1_output : 4'bz;  // Controlled_Buffer controlled_buffer_2

  // Notes on the sheet:
  //   Isabella Gonçales - 420120
endmodule

module Exercicio02 (
  input  [7:0] \input ,
  input  R_W,
  input  CS,
  input  clock,
  input  clear,
  output [7:0] \output 
);

  // Exercicio01 exercicio01_1: pin names not known; wires that end beside it: R_W, clock, CS, clear, \input [7:4], \output [7:4]
  // Exercicio01 exercicio01_2: pin names not known; wires that end beside it: R_W, clock, CS, clear, \input [3:0], \output [3:0]

  // Notes on the sheet:
  //   Isabella Gonçales - 420120
endmodule

module Exercicio03 (
  input  R_W,
  input  [7:0] \input ,
  input  [1:0] adress,
  input  CLR,
  output [7:0] \output 
);

  wire clock_1_out, decoder_1_out0, decoder_1_out1, decoder_1_out2, decoder_1_out3, not_1_out, not_2_out,
       not_3_out, not_4_out;

  Clock clock_1 (.out(clock_1_out));
  Decoder #(.select(2)) decoder_1 (
    .out0(decoder_1_out0), .out1(decoder_1_out1), .out2(decoder_1_out2), .out3(decoder_1_out3), .sel(adress));
  not not_1 (not_1_out, decoder_1_out0);
  not not_2 (not_2_out, decoder_1_out1);
  not not_3 (not_3_out, decoder_1_out2);
  not not_4 (not_4_out, decoder_1_out3);
  // Exercicio02 exercicio02_1: pin names not known; wires that end beside it: R_W, not_1_out, clock_1_out, CLR, \input , \output , \input 
  // Exercicio02 exercicio02_2: pin names not known; wires that end beside it: R_W, not_2_out, clock_1_out, CLR, \input , \output , \input 
  // Exercicio02 exercicio02_3: pin names not known; wires that end beside it: R_W, not_3_out, clock_1_out, CLR, \input , \output , \input 
  // Exercicio02 exercicio02_4: pin names not known; wires that end beside it: R_W, not_4_out, clock_1_out, CLR, \input , \output 

  // Notes on the sheet:
  //   Isabella Gonçales - 420120
endmodule

module Exercicio04 (
  input  R_W,
  input  [3:0] \input ,
  input  adress,
  input  clear,
  output [3:0] \output 
);

  wire clock_out, decoder_1_out0, decoder_1_out1, not_1_out, not_2_out;

  Clock clock (.out(clock_out));
  Decoder decoder_1 (.out0(decoder_1_out0), .out1(decoder_1_out1), .sel(adress));
  not not_1 (not_1_out, decoder_1_out0);
  not not_2 (not_2_out, decoder_1_out1);
  RAM1x4D ram1x4d_1 (.R_W(R_W), .CLK(clock_out), .CS(not_1_out), .clear(clear), .\input (\input ), .\output (\output ));
  RAM1x4D ram1x4d_2 (.R_W(R_W), .CLK(clock_out), .CS(not_2_out), .clear(clear), .\input (\input ), .\output (\output ));

  // Notes on the sheet:
  //   Isabella Gonçales - 420120
endmodule

module reg_D (
  input  [3:0] \input ,
  input  clock,
  input  clear,
  output [3:0] \output 
);

  D_Flip_Flop d_ff_1 (.clk(clock), .D(\input [3]), .Q(\output [3]), .reset(clear));  // open: Qn, preset, en
  D_Flip_Flop d_ff_2 (.clk(clock), .D(\input [2]), .Q(\output [2]), .reset(clear));  // open: Qn, preset, en
  D_Flip_Flop d_ff_3 (.clk(clock), .D(\input [1]), .Q(\output [1]), .reset(clear));  // open: Qn, preset, en
  D_Flip_Flop d_ff_4 (.clk(clock), .D(\input [0]), .Q(\output [0]), .reset(clear));  // open: Qn, preset, en

  // Notes on the sheet:
  //   Isabella Gonçales - 420120
endmodule

module RAM1x4D (
  input  [3:0] \input ,
  input  R_W,
  input  CLK,
  input  CS,
  input  clear,
  output [3:0] \output 
);

  wire and_1_out, and_2_out, not_1_out, not_2_out, not_3_out;
  wire [3:0] controlled_buffer_1_out, reg_d_1_output;

  not not_1 (not_1_out, R_W);
  not not_2 (not_2_out, CS);
  not not_3 (not_3_out, CS);
  and and_1 (and_1_out, not_1_out, not_2_out);
  assign controlled_buffer_1_out = and_1_out ? \input  : 4'bz;  // Controlled_Buffer controlled_buffer_1
  and and_2 (and_2_out, not_3_out, R_W);
  reg_D reg_d_1 (.\input (controlled_buffer_1_out), .clock(CLK), .clear(clear), .\output (reg_d_1_output));
  assign \output  = and_2_out ? reg_d_1_output : 4'bz;  // Controlled_Buffer controlled_buffer_2

  // Notes on the sheet:
  //   Isabella Gonçales - 420120
endmodule

module RAM1x8D (
  input  [7:0] \input ,
  input  R_W,
  input  CS,
  input  clock,
  input  clear,
  output [7:0] \output 
);

  RAM1x4D ram1x4d_1 (.R_W(R_W), .CLK(clock), .CS(CS), .clear(clear), .\input (\input [7:4]), .\output (\output [7:4]));
  RAM1x4D ram1x4d_2 (.R_W(R_W), .CLK(clock), .CS(CS), .clear(clear), .\input (\input [3:0]), .\output (\output [3:0]));

  // Notes on the sheet:
  //   Isabella Gonçales - 420120
endmodule

module Exercicio05 (
  input  R_W,
  input  [7:0] \input ,
  input  [1:0] adress,
  input  clear,
  output [7:0] \output 
);

  wire clock_1_out, decoder_1_out0, decoder_1_out1, decoder_1_out2, decoder_1_out3, not_1_out, not_2_out,
       not_3_out, not_4_out;

  Clock clock_1 (.out(clock_1_out));
  Decoder #(.select(2)) decoder_1 (
    .out0(decoder_1_out0), .out1(decoder_1_out1), .out2(decoder_1_out2), .out3(decoder_1_out3), .sel(adress));
  not not_1 (not_1_out, decoder_1_out0);
  not not_2 (not_2_out, decoder_1_out1);
  not not_3 (not_3_out, decoder_1_out2);
  not not_4 (not_4_out, decoder_1_out3);
  RAM1x8D ram1x8d_1 (
    .R_W(R_W), .CS(not_1_out), .clock(clock_1_out), .clear(clear), .\input (\input ), .\output (\output ));
  RAM1x8D ram1x8d_2 (
    .R_W(R_W), .CS(not_2_out), .clock(clock_1_out), .clear(clear), .\input (\input ), .\output (\output ));
  RAM1x8D ram1x8d_3 (
    .R_W(R_W), .CS(not_3_out), .clock(clock_1_out), .clear(clear), .\input (\input ), .\output (\output ));
  RAM1x8D ram1x8d_4 (
    .R_W(R_W), .CS(not_4_out), .clock(clock_1_out), .clear(clear), .\input (\input ), .\output (\output ));

  // Notes on the sheet:
  //   Isabella Gonçales - 420120
endmodule
