// Logisim project guia12.circ as structural Verilog: 9 circuits, main circuit reg JK
module reg_JK (
  input  [3:0] e,
  input  CLK,
  input  CLR,
  output [3:0] s
);

  wire not_1_out, not_2_out, not_3_out, not_4_out;

  J_K_Flip_Flop j_k_ff_1 (.J(e[3]), .clk(CLK), .K(not_1_out), .Q(s[3]), .reset(CLR));  // open: Qn, preset, en
  not not_1 (not_1_out, e[3]);
  J_K_Flip_Flop j_k_ff_2 (.J(e[2]), .clk(CLK), .K(not_2_out), .Q(s[2]), .reset(CLR));  // open: Qn, preset, en
  not not_2 (not_2_out, e[2]);
  J_K_Flip_Flop j_k_ff_3 (.J(e[1]), .clk(CLK), .K(not_3_out), .Q(s[1]), .reset(CLR));  // open: Qn, preset, en
  not not_3 (not_3_out, e[1]);
  J_K_Flip_Flop j_k_ff_4 (.J(e[0]), .clk(CLK), .K(not_4_out), .Q(s[0]), .reset(CLR));  // open: Qn, preset, en
  not not_4 (not_4_out, e[0]);

  // Notes on the sheet:
  //   Raphaela Fernanda Silva - 420141
endmodule

module exercicio01 (
  input  [3:0] e,
  input  R_W,
  input  CLK,
  input  CS,
  input  CLR,
  output [3:0] s
);

  wire and_1_out, and_2_out, not_1_out, not_2_out, not_3_out;
  wire [3:0] controlled_buffer_1_out, reg_jk_1_s;

  not not_1 (not_1_out, R_W);
  not not_2 (not_2_out, CS);
  not not_3 (not_3_out, CS);
  and and_1 (and_1_out, not_1_out, not_2_out);
  assign controlled_buffer_1_out = and_1_out ? e : 4'bz;  // Controlled_Buffer controlled_buffer_1
  and and_2 (and_2_out, not_3_out, R_W);
  reg_JK reg_jk_1 (.e(controlled_buffer_1_out), .CLK(CLK), .CLR(CLR), .s(reg_jk_1_s));
  assign s = and_2_out ? reg_jk_1_s : 4'bz;  // Controlled_Buffer controlled_buffer_2

  // Notes on the sheet:
  //   Raphaela Fernanda Silva - 420141
endmodule

module exercicio02 (
  input  [7:0] e,
  input  R_W,
  input  CS,
  input  CLK,
  input  CLR,
  output [7:0] s
);

  // exercicio01 exercicio01_1: pin names not known; wires that end beside it: R_W, CLK, CS, CLR, e[7:4], s[7:4]
  // exercicio01 exercicio01_2: pin names not known; wires that end beside it: R_W, CLK, CS, CLR, e[3:0], s[3:0]

  // Notes on the sheet:
  //   Raphaela Fernanda Silva - 420141
endmodule

module exercicio03 (
  input  R_W,
  input  [7:0] e,
  input  [1:0] adress,
  input  CLR,
  output [7:0] s
);

  wire clock_1_out, decoder_1_out0, decoder_1_out1, decoder_1_out2, decoder_1_out3, not_1_out, not_2_out,
       not_3_out, not_4_out;

  Clock clock_1 (.out(clock_1_out));
  Decoder #(.select(2)) decoder_1 (
    .out0(decoder_1_out0), .out1(decoder_1_out1), .out2(decoder_1_out2), .out3(decoder_1_out3), .sel(adress));
  not not_1 (not_1_out, decoder_1_out0);
  not not_2 (not_2_out, decoder_1_out1);
  not not_3 (not_3_out, decoder_1_out2);
  not not_4 (not_4_out, decoder_1_out3);
  // exercicio02 exercicio02_1: pin names not known; wires that end beside it: R_W, not_1_out, clock_1_out, CLR, e, s, e
  // exercicio02 exercicio02_2: pin names not known; wires that end beside it: R_W, not_2_out, clock_1_out, CLR, e, s, e
  // exercicio02 exercicio02_3: pin names not known; wires that end beside it: R_W, not_3_out, clock_1_out, CLR, e, s, e
  // exercicio02 exercicio02_4: pin names not known; wires that end beside it: R_W, not_4_out, clock_1_out, CLR, e, s

  // Notes on the sheet:
  //   Raphaela Fernanda Silva - 420141
endmodule

module exercicio04 (
  input  R_W,
  input  [3:0] e,
  input  adress,
  input  CLR,
  output [3:0] s
);

  wire CLK_out, decoder_1_out0, decoder_1_out1, not_1_out, not_2_out;

  Clock CLK (.out(CLK_out));
  Decoder decoder_1 (.out0(decoder_1_out0), .out1(decoder_1_out1), .sel(adress));
  not not_1 (not_1_out, decoder_1_out0);
  not not_2 (not_2_out, decoder_1_out1);
  RAM1x4D ram1x4d_1 (.R_W(R_W), .CLK(CLK_out), .CS(not_1_out), .CLR(CLR), .e(e), .s(s));
  RAM1x4D ram1x4d_2 (.R_W(R_W), .CLK(CLK_out), .CS(not_2_out), .CLR(CLR), .e(e), .s(s));

  // Notes on the sheet:
  //   Raphaela Fernanda Silva - 420141
endmodule

module reg_D (
  input  [3:0] e,
  input  CLK,
  input  CLR,
  output [3:0] s
);

  D_Flip_Flop d_ff_1 (.clk(CLK), .D(e[3]), .Q(s[3]), .reset(CLR));  // open: Qn, preset, en
  D_Flip_Flop d_ff_2 (.clk(CLK), .D(e[2]), .Q(s[2]), .reset(CLR));  // open: Qn, preset, en
  D_Flip_Flop d_ff_3 (.clk(CLK), .D(e[1]), .Q(s[1]), .reset(CLR));  // open: Qn, preset, en
  D_Flip_Flop d_ff_4 (.clk(CLK), .D(e[0]), .Q(s[0]), .reset(CLR));  // open: Qn, preset, en

  // Notes on the sheet:
  //   Raphaela Fernanda Silva - 420141
endmodule

module RAM1x4D (
  input  [3:0] e,
  input  R_W,
  input  CLK,
  input  CS,
  input  CLR,
  output [3:0] s
);

  wire and_1_out, and_2_out, not_1_out, not_2_out, not_3_out;
  wire [3:0] controlled_buffer_1_out, reg_d_1_s;

  not not_1 (not_1_out, R_W);
  not not_2 (not_2_out, CS);
  not not_3 (not_3_out, CS);
  and and_1 (and_1_out, not_1_out, not_2_out);
  assign controlled_buffer_1_out = and_1_out ? e : 4'bz;  // Controlled_Buffer controlled_buffer_1
  and and_2 (and_2_out, not_3_out, R_W);
  reg_D reg_d_1 (.e(controlled_buffer_1_out), .CLK(CLK), .CLR(CLR), .s(reg_d_1_s));
  assign s = and_2_out ? reg_d_1_s : 4'bz;  // Controlled_Buffer controlled_buffer_2

  // Notes on the sheet:
  //   Raphaela Fernanda Silva - 420141
endmodule

module RAM1x8D (
  input  [7:0] e,
  input  R_W,
  input  CS,
  input  CLK,
  input  CLR,
  output [7:0] s
);

  RAM1x4D ram1x4d_1 (.R_W(R_W), .CLK(CLK), .CS(CS), .CLR(CLR), .e(e[7:4]), .s(s[7:4]));
  RAM1x4D ram1x4d_2 (.R_W(R_W), .CLK(CLK), .CS(CS), .CLR(CLR), .e(e[3:0]), .s(s[3:0]));

  // Notes on the sheet:
  //   Raphaela Fernanda Silva -420141
endmodule

module exercicio05 (
  input  R_W,
  input  [7:0] e,
  input  [1:0] adress,
  input  CLR,
  output [7:0] s
);

  wire clock_1_out, decoder_1_out0, decoder_1_out1, decoder_1_out2, decoder_1_out3, not_1_out, not_2_out,
       not_3_out, not_4_out;

  Clock clock_1 (.out(clock_1_out));
  Decoder #(.select(2)) decoder_1 (
    .out0(decoder_1_out0), .out1(decoder_1_out1), .out2(decoder_1_out2), .out3(decoder_1_out3), .sel(adress));
  not not_1 (not_1_out, decoder_1_out0);
  not not_2 (not_2_out, decoder_1_out1);
  not not_3 (not_3_out, decoder_1_out2);
  not not_4 (not_4_out, decoder_1_out3);
  RAM1x8D ram1x8d_1 (.R_W(R_W), .CS(not_1_out), .CLK(clock_1_out), .CLR(CLR), .e(e), .s(s));
  RAM1x8D ram1x8d_2 (.R_W(R_W), .CS(not_2_out), .CLK(clock_1_out), .CLR(CLR), .e(e), .s(s));
  RAM1x8D ram1x8d_3 (.R_W(R_W), .CS(not_3_out), .CLK(clock_1_out), .CLR(CLR), .e(e), .s(s));
  RAM1x8D ram1x8d_4 (.R_W(R_W), .CS(not_4_out), .CLK(clock_1_out), .CLR(CLR), .e(e), .s(s));

  // Notes on the sheet:
  //   Raphaela Fernanda Silva - 420141
endmodule
