// Logisim project Guia12.circ as structural Verilog: 9 circuits, main circuit REG JK
module REG_JK (
  input  [3:0] Entrada,
  input  CLK,
  input  CLR,
  output [3:0] Saida
);

  wire not_1_out, not_2_out, not_3_out, not_4_out;

  J_K_Flip_Flop j_k_ff_1 (.J(Entrada[3]), .clk(CLK), .K(not_1_out), .Q(Saida[3]), .reset(CLR));  // open: Qn, preset, en
  not not_1 (not_1_out, Entrada[3]);
  J_K_Flip_Flop j_k_ff_2 (.J(Entrada[2]), .clk(CLK), .K(not_2_out), .Q(Saida[2]), .reset(CLR));  // open: Qn, preset, en
  not not_2 (not_2_out, Entrada[2]);
  J_K_Flip_Flop j_k_ff_3 (.J(Entrada[1]), .clk(CLK), .K(not_3_out), .Q(Saida[1]), .reset(CLR));  // open: Qn, preset, en
  not not_3 (not_3_out, Entrada[1]);
  J_K_Flip_Flop j_k_ff_4 (.J(Entrada[0]), .clk(CLK), .K(not_4_out), .Q(Saida[0]), .reset(CLR));  // open: Qn, preset, en
  not not_4 (not_4_out, Entrada[0]);

  // Notes on the sheet:
  //   Caio Ragacci Pimentel - 405794
  //   Registrador JK
endmodule

module guia12_01 (
  input  [3:0] Entrada,
  input  R_W,
  input  CLK,
  input  CS,
  input  CLR,
  output [3:0] Saida
);

  wire and_1_out, and_2_out, not_1_out, not_2_out, not_3_out;
  wire [3:0] controlled_buffer_1_out, reg_jk_1_saida;

  not not_1 (not_1_out, R_W);
  not not_2 (not_2_out, CS);
  not not_3 (not_3_out, CS);
  and and_1 (and_1_out, not_1_out, not_2_out);
  assign controlled_buffer_1_out = and_1_out ? Entrada : 4'bz;  // Controlled_Buffer controlled_buffer_1
  REG_JK reg_jk_1 (.CLK(CLK), .Entrada(controlled_buffer_1_out), .CLR(CLR), .Saida(reg_jk_1_saida));
  and and_2 (and_2_out, not_3_out, R_W);
  assign Saida = and_2_out ? reg_jk_1_saida : 4'bz;  // Controlled_Buffer controlled_buffer_2

  // Notes on the sheet:
  //   Caio Ragacci Pimentel - 405794
  //   Guia12 - 01
endmodule

module guia12_02 (
  input  [7:0] Entrada,
  input  R_W,
  input  CS,
  input  CLK,
  input  CLR,
  output [7:0] Saida
);

  RAM_1_x_4D ram_1_x_4d_1 (.R_W(R_W), .CLK(CLK), .CS(CS), .CLR(CLR));  // open: Entrada, Saida
  RAM_1_x_4D ram_1_x_4d_2 (.R_W(R_W), .CLK(CLK), .CS(CS), .CLR(CLR));  // open: Entrada, Saida

  // Notes on the sheet:
  //   Caio Ragacci Pimentel - 405794
  //   Guia12 - 02
endmodule

module guia12_03 (
  input  R_W,
  input  [7:0] Entrada,
  input  [1:0] Adress,
  input  CLR,
  output [7:0] Saida
);

  wire CLK_out, decoder_1_out0, decoder_1_out1, decoder_1_out2, decoder_1_out3, not_1_out, not_2_out,
       not_3_out, not_4_out;

  Clock CLK (.out(CLK_out));
  Decoder #(.select(2)) decoder_1 (
    .out0(decoder_1_out0), .out1(decoder_1_out1), .out2(decoder_1_out2), .out3(decoder_1_out3), .sel(Adress));
  not not_1 (not_1_out, decoder_1_out0);
  not not_2 (not_2_out, decoder_1_out1);
  not not_3 (not_3_out, decoder_1_out2);
  not not_4 (not_4_out, decoder_1_out3);
  RAM_1_x_8D ram_1_x_8d_1 (.R_W(R_W), .CS(not_4_out), .CLK(CLK_out), .CLR(CLR), .Entrada(Entrada), .Saida(Saida));
  RAM_1_x_8D ram_1_x_8d_2 (.R_W(R_W), .CS(not_1_out), .CLK(CLK_out), .CLR(CLR), .Entrada(Entrada), .Saida(Saida));
  RAM_1_x_8D ram_1_x_8d_3 (.R_W(R_W), .CS(not_2_out), .CLK(CLK_out), .CLR(CLR), .Entrada(Entrada), .Saida(Saida));
  RAM_1_x_8D ram_1_x_8d_4 (.R_W(R_W), .CS(not_3_out), .CLK(CLK_out), .CLR(CLR), .Entrada(Entrada), .Saida(Saida));

  // Notes on the sheet:
  //   Caio Ragacci Pimentel - 405794
  //   Guia12 - 03
endmodule

module guia12_04 (
  input  R_W,
  input  [3:0] Entrada,
  input  Adress,
  input  CLR,
  output [3:0] Saida
);

  wire CLK_out, decoder_1_out0, decoder_1_out1, not_1_out, not_2_out;

  Clock CLK (.out(CLK_out));
  Decoder decoder_1 (.out0(decoder_1_out0), .out1(decoder_1_out1), .sel(Adress));
  not not_1 (not_1_out, decoder_1_out0);
  not not_2 (not_2_out, decoder_1_out1);
  RAM_1_x_4D ram_1_x_4d_1 (.R_W(R_W), .CLK(CLK_out), .CS(not_1_out), .CLR(CLR));  // open: Entrada, Saida
  RAM_1_x_4D ram_1_x_4d_2 (.R_W(R_W), .CLK(CLK_out), .CS(not_2_out), .CLR(CLR));  // open: Entrada, Saida

  // Notes on the sheet:
  //   Caio Ragacci Pimentel - 405794
  //   Guia12 - 04
endmodule

module guia12_05 (
  input  [7:0] Entrada,
  input  R_W,
  input  [1:0] Adress,
  input  CLR,
  output [7:0] Saida
);

  wire CLK_out, decoder_1_out0, decoder_1_out1, decoder_1_out2, decoder_1_out3, not_1_out, not_2_out,
       not_3_out, not_4_out;

  Clock CLK (.out(CLK_out));
  Decoder #(.select(2)) decoder_1 (
    .out0(decoder_1_out0), .out1(decoder_1_out1), .out2(decoder_1_out2), .out3(decoder_1_out3), .sel(Adress));
  not not_1 (not_1_out, decoder_1_out0);
  not not_2 (not_2_out, decoder_1_out1);
  not not_3 (not_3_out, decoder_1_out2);
  not not_4 (not_4_out, decoder_1_out3);
  RAM_1_x_8D ram_1_x_8d_1 (.R_W(R_W), .CS(not_1_out), .CLK(CLK_out), .CLR(CLR), .Entrada(Entrada), .Saida(Saida));
  RAM_1_x_8D ram_1_x_8d_2 (.R_W(R_W), .CS(not_2_out), .CLK(CLK_out), .CLR(CLR), .Entrada(Entrada), .Saida(Saida));
  RAM_1_x_8D ram_1_x_8d_3 (.R_W(R_W), .CS(not_3_out), .CLK(CLK_out), .CLR(CLR), .Entrada(Entrada), .Saida(Saida));
  RAM_1_x_8D ram_1_x_8d_4 (.R_W(R_W), .CS(not_4_out), .CLK(CLK_out), .CLR(CLR), .Entrada(Entrada), .Saida(Saida));

  // Notes on the sheet:
  //   Caio Ragacci Pimentel - 405794
  //   Guia12 - 05
endmodule

module REG_D (
  input  [3:0] Entrada,
  input  CLK,
  input  CLR,
  output [3:0] Saida
);

  D_Flip_Flop d_ff_1 (.clk(CLK), .D(Entrada[3]), .Q(Saida[3]), .reset(CLR));  // open: Qn, preset, en
  D_Flip_Flop d_ff_2 (.clk(CLK), .D(Entrada[2]), .Q(Saida[2]), .reset(CLR));  // open: Qn, preset, en
  D_Flip_Flop d_ff_3 (.clk(CLK), .D(Entrada[1]), .Q(Saida[1]), .reset(CLR));  // open: Qn, preset, en
  D_Flip_Flop d_ff_4 (.clk(CLK), .D(Entrada[0]), .Q(Saida[0]), .reset(CLR));  // open: Qn, preset, en

  // Notes on the sheet:
  //   Caio Ragacci Pimentel - 405794
endmodule

module RAM_1_x_4D (
  input  [3:0] Entrada,
  input  R_W,
  input  CLK,
  input  CS,
  input  CLR,
  output [3:0] Saida
);

  wire and_1_out, and_2_out, not_1_out, not_2_out, not_3_out;
  wire [3:0] controlled_buffer_1_out, reg_d_1_saida;

  not not_1 (not_1_out, R_W);
  not not_2 (not_2_out, CS);
  not not_3 (not_3_out, CS);
  and and_1 (and_1_out, not_1_out, not_2_out);
  assign controlled_buffer_1_out = and_1_out ? Entrada : 4'bz;  // Controlled_Buffer controlled_buffer_1
  REG_D reg_d_1 (.CLK(CLK), .Entrada(controlled_buffer_1_out), .CLR(CLR), .Saida(reg_d_1_saida));
  and and_2 (and_2_out, not_3_out, R_W);
  assign Saida = and_2_out ? reg_d_1_saida : 4'bz;  // Controlled_Buffer controlled_buffer_2

  // Notes on the sheet:
  //   Caio Ragacci Pimentel - 405794
endmodule

module RAM_1_x_8D (
  input  [7:0] Entrada,
  input  R_W,
  input  CS,
  input  CLK,
  input  CLR,
  output [7:0] Saida
);

  RAM_1_x_4D ram_1_x_4d_1 (.R_W(R_W), .CLK(CLK), .CS(CS), .CLR(CLR));  // open: Entrada, Saida
  RAM_1_x_4D ram_1_x_4d_2 (.R_W(R_W), .CLK(CLK), .CS(CS), .CLR(CLR));  // open: Entrada, Saida

  // Notes on the sheet:
  //   Caio Ragacci Pimentel - 405794
endmodule
