// Logisim project GUIA12 CORRIGIDO.circ as structural Verilog: 9 circuits, main circuit REG JK
module REG_JK (
  input  [3:0] Entrada,
  input  CLK,
  input  CLR,
  output [3:0] Saida
);

  wire not_1_out, not_2_out, not_3_out, not_4_out;

  J_K_Flip_Flop j_k_ff_1 (.J(Entrada[3]), .clk(CLK), .K(not_1_out), .Q(Saida[3]), .reset(CLR));  // open: Qn, preset, en
  not not_1 (not_1_out, Entrada[3]);
  J_K_Flip_Flop j_k_ff_2 (.J(Entrada[2]), .clk(CLK), .K(not_2_out), .Q(Saida[2]), .reset(CLR));  // open: Qn, preset, en
  not not_2 (not_2_out, Entrada[2]);
  J_K_Flip_Flop j_k_ff_3 (.J(Entrada[1]), .clk(CLK), .K(not_3_out), .Q(Saida[1]), .reset(CLR));  // open: Qn, preset, en
  not not_3 (not_3_out, Entrada[1]);
  J_K_Flip_Flop j_k_ff_4 (.J(Entrada[0]), .clk(CLK), .K(not_4_out), .Q(Saida[0]), .reset(CLR));  // open: Qn, preset, en
  not not_4 (not_4_out, Entrada[0]);
endmodule

module EX01_RAM1X4 (
  input  [3:0] Entrada,
  input  R_W,
  input  CLK,
  input  CS,
  input  CLR,
  output [3:0] Saida
);

  wire and_1_out, and_2_out, not_1_out, not_2_out, not_3_out;
  wire [3:0] controlled_buffer_1_out, reg_jk_1_saida;

  not not_1 (not_1_out, R_W);
  not not_2 (not_2_out, CS);
  not not_3 (not_3_out, CS);
  and and_1 (and_1_out, not_1_out, not_2_out);
  assign controlled_buffer_1_out = and_1_out ? Entrada : 4'bz;  // Controlled_Buffer controlled_buffer_1
  and and_2 (and_2_out, not_3_out, R_W);
  REG_JK reg_jk_1 (.Entrada(controlled_buffer_1_out), .CLK(CLK), .CLR(CLR), .Saida(reg_jk_1_saida));
  assign Saida = and_2_out ? reg_jk_1_saida : 4'bz;  // Controlled_Buffer controlled_buffer_2
endmodule

module EX02_RAM1X8 (
  input  [7:0] Entrada,
  input  R_W,
  input  CS,
  input  CLK,
  input  CLR,
  output [7:0] Saida
);

  // EX01_RAM1X4 ex01_ram1x4_1: pin names not known; wires that end beside it: R_W, CLK, CS, CLR, Entrada[7:4], Saida[7:4]
  // EX01_RAM1X4 ex01_ram1x4_2: pin names not known; wires that end beside it: R_W, CLK, CS, CLR, Entrada[3:0], Saida[3:0]
endmodule

module EX03_RAM4X8 (
  input  R_W,
  input  [7:0] Entrada,
  input  [1:0] adress,
  input  CLR,
  output [7:0] Saida
);

  wire clock_1_out, decoder_1_out0, decoder_1_out1, decoder_1_out2, decoder_1_out3, not_1_out, not_2_out,
       not_3_out, not_4_out;

  Clock clock_1 (.out(clock_1_out));
  Decoder #(.select(2)) decoder_1 (
    .out0(decoder_1_out0), .out1(decoder_1_out1), .out2(decoder_1_out2), .out3(decoder_1_out3), .sel(adress));
  not not_1 (not_1_out, decoder_1_out0);
  not not_2 (not_2_out, decoder_1_out1);
  not not_3 (not_3_out, decoder_1_out2);
  not not_4 (not_4_out, decoder_1_out3);
  // EX02_RAM1X8 ex02_ram1x8_1: pin names not known; wires that end beside it: R_W, not_1_out, clock_1_out, CLR, Entrada, Saida, Entrada
  // EX02_RAM1X8 ex02_ram1x8_2: pin names not known; wires that end beside it: R_W, not_2_out, clock_1_out, CLR, Entrada, Saida, Entrada
  // EX02_RAM1X8 ex02_ram1x8_3: pin names not known; wires that end beside it: R_W, not_3_out, clock_1_out, CLR, Entrada, Saida, Entrada
  // EX02_RAM1X8 ex02_ram1x8_4: pin names not known; wires that end beside it: R_W, not_4_out, clock_1_out, CLR, Entrada, Saida
endmodule

module REG_D (
  input  [3:0] Entrada,
  input  CLK,
  input  CLR,
  output [3:0] Saida
);

  D_Flip_Flop d_ff_1 (.clk(CLK), .D(Entrada[3]), .Q(Saida[3]), .reset(CLR));  // open: Qn, preset, en
  D_Flip_Flop d_ff_2 (.clk(CLK), .D(Entrada[2]), .Q(Saida[2]), .reset(CLR));  // open: Qn, preset, en
  D_Flip_Flop d_ff_3 (.clk(CLK), .D(Entrada[1]), .Q(Saida[1]), .reset(CLR));  // open: Qn, preset, en
  D_Flip_Flop d_ff_4 (.clk(CLK), .D(Entrada[0]), .Q(Saida[0]), .reset(CLR));  // open: Qn, preset, en
endmodule

module RAM1X4_D (
  input  [3:0] Entrada,
  input  R_W,
  input  CLK,
  input  CS,
  input  CLR,
  output [3:0] Saida
);

  wire and_1_out, and_2_out, not_1_out, not_2_out, not_3_out;
  wire [3:0] controlled_buffer_1_out, reg_d_1_saida;

  not not_1 (not_1_out, R_W);
  not not_2 (not_2_out, CS);
  not not_3 (not_3_out, CS);
  and and_1 (and_1_out, not_1_out, not_2_out);
  assign controlled_buffer_1_out = and_1_out ? Entrada : 4'bz;  // Controlled_Buffer controlled_buffer_1
  and and_2 (and_2_out, not_3_out, R_W);
  REG_D reg_d_1 (.Entrada(controlled_buffer_1_out), .CLK(CLK), .CLR(CLR), .Saida(reg_d_1_saida));
  assign Saida = and_2_out ? reg_d_1_saida : 4'bz;  // Controlled_Buffer controlled_buffer_2
endmodule

module EX04_RAM2X4 (
  input  R_W,
  input  [3:0] Entrada,
  input  adress,
  input  CLR,
  output [3:0] Saida
);

  wire CLK_out, decoder_1_out0, decoder_1_out1, not_1_out, not_2_out;

  Clock CLK (.out(CLK_out));
  Decoder decoder_1 (.out0(decoder_1_out0), .out1(decoder_1_out1), .sel(adress));
  not not_1 (not_1_out, decoder_1_out0);
  not not_2 (not_2_out, decoder_1_out1);
  RAM1X4_D ram1x4_d_1 (.R_W(R_W), .CLK(CLK_out), .CS(not_1_out), .CLR(CLR), .Entrada(Entrada), .Saida(Saida));
  RAM1X4_D ram1x4_d_2 (.R_W(R_W), .CLK(CLK_out), .CS(not_2_out), .CLR(CLR), .Entrada(Entrada), .Saida(Saida));
endmodule

module RAM1X8D (
  input  [7:0] Entrada,
  input  R_W,
  input  CS,
  input  CLK,
  input  CLR,
  output [7:0] Saida
);

  RAM1X4_D ram1x4_d_1 (.R_W(R_W), .CLK(CLK), .CS(CS), .CLR(CLR), .Entrada(Entrada[7:4]), .Saida(Saida[7:4]));
  RAM1X4_D ram1x4_d_2 (.R_W(R_W), .CLK(CLK), .CS(CS), .CLR(CLR), .Entrada(Entrada[3:0]), .Saida(Saida[3:0]));
endmodule

module EX05_RAM4X8D (
  input  R_W,
  input  [7:0] Entrada,
  input  [1:0] adress,
  input  CLR,
  output [7:0] Saida
);

  wire clock_1_out, decoder_1_out0, decoder_1_out1, decoder_1_out2, decoder_1_out3, not_1_out, not_2_out,
       not_3_out, not_4_out;

  Clock clock_1 (.out(clock_1_out));
  Decoder #(.select(2)) decoder_1 (
    .out0(decoder_1_out0), .out1(decoder_1_out1), .out2(decoder_1_out2), .out3(decoder_1_out3), .sel(adress));
  not not_1 (not_1_out, decoder_1_out0);
  not not_2 (not_2_out, decoder_1_out1);
  not not_3 (not_3_out, decoder_1_out2);
  not not_4 (not_4_out, decoder_1_out3);
  RAM1X8D ram1x8d_1 (.R_W(R_W), .CS(not_1_out), .CLK(clock_1_out), .CLR(CLR), .Entrada(Entrada), .Saida(Saida));
  RAM1X8D ram1x8d_2 (.R_W(R_W), .CS(not_2_out), .CLK(clock_1_out), .CLR(CLR), .Entrada(Entrada), .Saida(Saida));
  RAM1X8D ram1x8d_3 (.R_W(R_W), .CS(not_3_out), .CLK(clock_1_out), .CLR(CLR), .Entrada(Entrada), .Saida(Saida));
  RAM1X8D ram1x8d_4 (.R_W(R_W), .CS(not_4_out), .CLK(clock_1_out), .CLR(CLR), .Entrada(Entrada), .Saida(Saida));
endmodule
