// Logisim project s0_s1_s2.circ as structural Verilog: 1 circuit, main circuit main
module main (
  input  a,
  input  b,
  input  c,
  input  d,
  input  a_2,
  input  b_2,
  input  c_2,
  input  d_2,
  input  a_3,
  input  b_3,
  input  c_3,
  input  d_3,
  output s0,
  output s1,
  output s2
);

  wire and_1_out, and_2_out, and_3_out, and_4_out, and_5_out, and_6_out, and_7_out, and_8_out, and_9_out,
       and_10_out, not_1_out, not_2_out, not_3_out, not_4_out, not_5_out, not_6_out, not_7_out, not_8_out;

  not not_1 (not_1_out, a);
  not not_2 (not_2_out, b);
  not not_3 (not_3_out, a_2);
  not not_4 (not_4_out, b_2);
  not not_5 (not_5_out, c_2);
  not not_6 (not_6_out, d_2);
  not not_7 (not_7_out, c_3);
  not not_8 (not_8_out, d_3);
  and and_1 (and_1_out, not_1_out, c);
  and and_2 (and_2_out, not_2_out, c, d);
  and and_3 (and_3_out, not_1_out, not_2_out, d);
  and and_4 (and_4_out, not_3_out, not_4_out, not_5_out, not_6_out);
  and and_5 (and_5_out, not_3_out, not_5_out, b_2, d_2);
  and and_6 (and_6_out, a_2, c_2, not_4_out, not_6_out);
  and and_7 (and_7_out, a_2, b_2, c_2, d_2);
  and and_8 (and_8_out, a_3, not_7_out);
  and and_9 (and_9_out, not_7_out, b_3, not_8_out);
  buf and_10 (and_10_out, a_3);  // AND_Gate
  or or_1 (s2, and_8_out, and_9_out, and_10_out);
  or or_2 (s0, and_1_out, and_2_out, and_3_out);
  or or_3 (s1, and_4_out, and_5_out, and_6_out, and_7_out);
endmodule
