// Logisim project ExercicioL.circ as structural Verilog: 2 circuits, main circuit main
module main (
  input  in_1,
  input  in_2,
  input  in_3,
  input  in_4,
  input  in_5,
  input  in_6,
  input  in_7,
  input  in_8,
  input  in_9,
  input  in_10,
  input  in_11,
  input  in_12,
  input  in_13,
  input  in_14,
  input  in_15,
  input  in_16,
  output out_17,
  output out_18,
  output out_19,
  output out_20
);

  CalculaS0 calculas0_1 (.in_1(in_1), .in_2(in_5), .in_3(in_9), .in_4(in_13), .out_5(out_17));
  CalculaS0 calculas0_2 (.in_1(in_2), .in_2(in_6), .in_3(in_10), .in_4(in_14), .out_5(out_18));
  CalculaS0 calculas0_3 (.in_1(in_3), .in_2(in_7), .in_3(in_11), .in_4(in_15), .out_5(out_19));
  CalculaS0 calculas0_4 (.in_1(in_4), .in_2(in_8), .in_3(in_12), .in_4(in_16), .out_5(out_20));
endmodule

module CalculaS0 (
  input  in_1,
  input  in_2,
  input  in_3,
  input  in_4,
  output out_5
);

  wire and_1_out, not_1_out, not_2_out, or_1_out;

  not not_1 (not_1_out, in_1);
  not not_2 (not_2_out, in_2);
  and and_1 (and_1_out, not_2_out, in_4);
  or or_1 (or_1_out, and_1_out, in_3);
  and and_2 (out_5, not_1_out, or_1_out);
endmodule
