// Logisim project CorreçãoDaProva.circ as structural Verilog: 1 circuit, main circuit main
module main (
  input  a,
  input  b,
  input  c,
  input  d,
  output out_5
);

  wire and_1_out, and_2_out, and_3_out, and_4_out, and_5_out, and_6_out, and_7_out, and_8_out, and_9_out,
       and_10_out, not_1_out, not_2_out, not_3_out, not_4_out, not_5_out, not_6_out, not_7_out, not_8_out,
       not_9_out, not_10_out, not_11_out, not_12_out, not_13_out, not_14_out, not_15_out, not_16_out,
       or_1_out, or_2_out, or_3_out;

  not not_1 (not_1_out, c);
  not not_2 (not_2_out, d);
  not not_3 (not_3_out, c);
  not not_4 (not_4_out, d);
  not not_5 (not_5_out, a);
  not not_6 (not_6_out, b);
  not not_7 (not_7_out, c);
  not not_8 (not_8_out, d);
  not not_9 (not_9_out, a);
  not not_10 (not_10_out, c);
  not not_11 (not_11_out, b);
  not not_12 (not_12_out, d);
  not not_13 (not_13_out, a);
  not not_14 (not_14_out, b);
  not not_15 (not_15_out, a);
  not not_16 (not_16_out, b);
  and and_1 (and_1_out, not_1_out, not_2_out, b);
  and and_2 (and_2_out, a, not_3_out);
  and and_3 (and_3_out, b, a, not_4_out);
  and and_4 (and_4_out, not_5_out, not_6_out, not_7_out, not_7_out, not_8_out);
  and and_5 (and_5_out, not_9_out, b, not_10_out, d);
  and and_6 (and_6_out, a, b, c, d);
  and and_7 (and_7_out, not_11_out, a, not_12_out, c);
  and and_8 (and_8_out, d, not_13_out, not_14_out);
  and and_9 (and_9_out, not_15_out, c);
  and and_10 (and_10_out, not_16_out, c, d);
  or or_1 (or_1_out, and_1_out, and_2_out, and_3_out);
  or or_2 (or_2_out, and_4_out, and_5_out, and_6_out, and_7_out);
  or or_3 (or_3_out, and_8_out, and_9_out, and_10_out);
  or or_4 (out_5, or_1_out, or_2_out, or_3_out);

  // Notes on the sheet:
  //                                  ----------------------------s2-------------------------------
  //   -----------------------------------s1-------------------------------
  //             ------------------------s0------------------------------
  //   Lorena Danielle Gonçalves Bento - 435049
  //                                         s1: a'b'c'd' + a'bc'd + abcd + ab'cd'
  //   s2: bc'd' + ac' + abd'
  //   s0: a'b'd + a'c + b'cd                  
endmodule
