// Logisim project LetraJ.circ as structural Verilog: 1 circuit, main circuit main
// 1
module main (
  input  a,
  input  b,
  input  c,
  input  d,
  output s2
);

  wire and1_out, and2_out, and3_out, and4_2_out, and4_out, not1_out, not2_out, or1_out;

  not not1 (not1_out, c);
  not not2 (not2_out, d);
  and and2 (and2_out, b, not1_out);
  and and1 (and1_out, a, b);
  and and3 (and3_out, and2_out, not2_out);
  and and4 (and4_out, and1_out, not2_out);
  or or1 (or1_out, and4_out, and3_out);
  and and4_2 (and4_2_out, a, not1_out);
  or or2 (s2, or1_out, and4_2_out);

  // Notes on the sheet:
  //   w1
  //   Mateus Augusto Moraes Ferreira   Matricula:435669
  //   Circuito Letra j.)
  //   w3
  //   w2
  //   w4
  //   s1
  //   w5
endmodule
