// Logisim project LetraK.circ as structural Verilog: 1 circuit, main circuit main
module main (
  input  a,
  input  b,
  input  c,
  input  d,
  output out_5
);

  wire xnor_1_out, xnor_2_out;

  xnor xnor_1 (xnor_1_out, a, c);
  xnor xnor_2 (xnor_2_out, b, d);
  and and_1 (out_5, xnor_1_out, xnor_2_out);

  // Notes on the sheet:
  //   Mateus Augusto Moraes Ferreira   Matricula:435669
  //   Circuito letra k. )
  //   w1
  //   w2
endmodule
