// Logisim project LetraL.circ as structural Verilog: 1 circuit, main circuit main
module main (
  input  a,
  input  b,
  input  c,
  input  d,
  output s0
);

  wire and_1_out, not_1_out, not_2_out, or_1_out;

  not not_1 (not_1_out, a);
  not not_2 (not_2_out, b);
  and and_1 (and_1_out, not_2_out, d);
  or or_1 (or_1_out, and_1_out, c);
  and and_2 (s0, not_1_out, or_1_out);

  // Notes on the sheet:
  //   Circuito Letra L .)
  //   w1
  //   Mateus Augusto Moraes Ferreira   Matricula:435669
  //   w2
endmodule
