// Logisim project Extras 6 e 7.circ as structural Verilog: 1 circuit, main circuit main
module main (
  input  A,
  input  B,
  input  A_2,
  input  B_2,
  output S,
  output S_2
);

  nor NOR (S, A, B);
  or OR (S_2, A_2, B_2);

  // Notes on the sheet:
  //   Exercício 06 - Extras
  //   Exercício 07 - Extras
endmodule
