// Logisim project extra2.circ as structural Verilog
module main (
  input  in_1,
  input  in_2,
  input  in_3,
  input  in_4,
  input  in_5,
  input  in_6,
  input  in_7,
  input  in_8,
  output out_9
);

  or or_1 (out_9, in_1, in_2, in_3, in_4, in_5, in_6, in_7, in_8);

  // Notes on the sheet:
  //   Gabriel Benjamim de Carvalho
endmodule
