// Logisim project Extras.circ as structural Verilog: 1 circuit, main circuit main
module main (
  input  a,
  input  b,
  input  c,
  input  a_2,
  input  b_2,
  input  c_2,
  output s,
  output s_2
);

  NotExactlyOne xnor_1 (.out(s), .in0(a), .in1(b), .in2(c));
  or or_1 (s_2, a_2, b_2, c_2);

  // Notes on the sheet:
  //   Retorna 1, se todos os seus bits forem iguais a 0
  //   Retorna 1, se algum de seus bits for igual a 1
endmodule
