// Logisim project Exemplo0009.circ as structural Verilog: 2 circuits, main circuit main
module main (
  input  A,
  input  B,
  input  C,
  output out_4
);

  and and_1 (out_4, A, B, C);
endmodule

module Exemplo0009 (
  input  A,
  input  B,
  input  C,
  output S
);

  wire not_1_out, not_2_out, not_3_out, or_1_out;

  not not_1 (not_1_out, A);
  not not_2 (not_2_out, B);
  not not_3 (not_3_out, C);
  or or_1 (or_1_out, not_1_out, not_2_out, not_3_out);
  not not_4 (S, or_1_out);
endmodule
