// Logisim project Extra01.circ as structural Verilog: 1 circuit, main circuit main
module main (
  input  A,
  input  B,
  input  C,
  input  D,
  input  E,
  input  F,
  input  G,
  input  H,
  output S
);

  wire S1_out, S2_out, S3_out, S4_out, S5_out;

  buf S2 (S2_out, D);
  or S3 (S3_out, S2_out, E, F);
  and S1 (S1_out, A, B, C);
  nor S4 (S4_out, G, H);
  nand S5 (S5_out, S1_out, S3_out);
  xnor xnor_1 (S, S5_out, S4_out);
endmodule
