// Logisim project Extra02.circ as structural Verilog: 1 circuit, main circuit main
module main (
  input  A,
  input  B,
  input  C,
  input  D,
  input  E,
  input  F,
  input  G,
  input  H,
  output S
);

  wire or_1_out, or_2_out, or_3_out, or_4_out;

  or or_1 (or_1_out, A, B);
  or or_2 (or_2_out, C, D);
  or or_3 (or_3_out, E, F);
  or or_4 (or_4_out, G, H);
  or or_5 (S, or_1_out, or_2_out, or_3_out, or_4_out);
endmodule
