// Logisim project nand 2 entradas.circ as structural Verilog: 3 circuits, main circuit NAND
module NAND (
  input  in_1,
  input  in_2,
  output out_3
);

  \not  not_1 (.a(in_2), .b(in_1), .out_3(out_3));
endmodule

module \and  (
  input  a,
  input  b,
  output s
);

  and and_1 (s, a, b);
endmodule

module \not  (
  input  a,
  input  b,
  output out_3
);

  wire and_1_s;

  \and  and_1 (.a(a), .b(b), .s(and_1_s));
  not not_1 (out_3, and_1_s);
endmodule
