// Logisim project nor com 2 entradas.circ as structural Verilog: 3 circuits, main circuit nor
module \nor  (
  input  a,
  input  b,
  output s
);

  wire or_1_s;

  \or  or_1 (.a(a), .b(b), .s(or_1_s));
  \not  not_1 (.in_1(or_1_s), .s(s));
endmodule

module \or  (
  input  a,
  input  b,
  output s
);

  or or_1 (s, a, b);
endmodule

module \not  (
  input  in_1,
  output s
);

  not not_1 (s, in_1);
endmodule
