// Logisim project NOR.circ as structural Verilog: 1 circuit, main circuit main
module main (
  input  a,
  input  b,
  input  c,
  input  d,
  input  e,
  input  f,
  input  g,
  input  h,
  output s
);

  nor NOR (s, a, b, c, d, e, f, g, h);
endmodule
