// Logisim project exercicio 6.circ as structural Verilog: 1 circuit, main circuit main
module main (
  input  in_1,
  input  in_2,
  input  in_3,
  input  in_4,
  input  in_5,
  input  in_6,
  input  in_7,
  input  in_8,
  output out_9
);

  wire OR3_out, OR4_out, OR_1_out, OR_2_out, OR_5_out, OR_6_out, OR_7_out;

  or OR_1 (OR_1_out, in_1, in_2);
  or OR_2 (OR_2_out, OR_1_out, in_3);
  or OR3 (OR3_out, OR_2_out, in_4);
  or OR4 (OR4_out, OR3_out, in_5);
  or OR_5 (OR_5_out, OR4_out, in_6);
  or OR_6 (OR_6_out, OR_5_out, in_7);
  or OR_7 (OR_7_out, OR_6_out, in_8);
  not not_1 (out_9, OR_7_out);
endmodule
