// Logisim project exerciciobyte.circ as structural Verilog: 2 circuits, main circuit main
module main (
  input  in_1,
  input  in_2,
  input  in_3,
  input  in_4,
  input  in_5,
  input  in_6,
  input  in_7,
  input  in_8,
  output out_9
);

  wire and_1_out, and_3_out, not_1_out, not_2_out, not_3_out, not_4_out, not_5_out, not_6_out, not_7_out,
       not_8_out;

  not not_1 (not_1_out, in_2);
  not not_2 (not_2_out, in_1);
  not not_3 (not_3_out, in_3);
  not not_4 (not_4_out, in_4);
  and and_1 (and_1_out, not_2_out, not_1_out, not_3_out, not_4_out);
  not not_5 (not_5_out, in_5);
  and and_2 (out_9, and_1_out, and_3_out);
  not not_6 (not_6_out, in_6);
  not not_7 (not_7_out, in_7);
  and and_3 (and_3_out, not_5_out, not_6_out, not_7_out, not_8_out);
  not not_8 (not_8_out, in_8);
endmodule

// TESTE
module teste (
  input  in_1,
  input  in_2,
  input  in_3,
  input  in_4,
  input  in_5,
  input  in_6,
  input  in_7,
  input  in_8,
  output out_9
);

  wire clock_1_out, clock_2_out, clock_3_out, clock_4_out, clock_5_out, clock_6_out, clock_7_out,
       clock_8_out, not_1_out, not_2_out, not_3_out, not_4_out, not_5_out, not_6_out, not_7_out, not_8_out,
       or_1_out, or_2_out, or_3_out, or_4_out, or_5_out, or_6_out, or_7_out, or_8_out;

  or or_1 (or_1_out, in_1, clock_1_out);
  not not_1 (not_1_out, or_1_out);
  or or_2 (or_2_out, in_2, clock_3_out);
  or or_3 (or_3_out, in_3, clock_5_out);
  not not_2 (not_2_out, or_3_out);
  not not_3 (not_3_out, or_2_out);
  or or_4 (or_4_out, in_4, clock_4_out);
  or or_5 (or_5_out, in_5, clock_2_out);
  not not_4 (not_4_out, or_5_out);
  not not_5 (not_5_out, or_4_out);
  and and_1 (out_9, not_1_out, not_3_out, not_2_out, not_5_out, not_4_out, not_7_out, not_6_out, not_8_out);
  or or_6 (or_6_out, in_7, clock_6_out);
  or or_7 (or_7_out, in_6, clock_8_out);
  not not_6 (not_6_out, or_6_out);
  not not_7 (not_7_out, or_7_out);
  or or_8 (or_8_out, in_8, clock_7_out);
  not not_8 (not_8_out, or_8_out);
  Clock #(.highDuration(128), .lowDuration(128)) clock_1 (.out(clock_1_out));
  Clock #(.highDuration(8), .lowDuration(4)) clock_2 (.out(clock_2_out));
  Clock #(.highDuration(64), .lowDuration(7)) clock_3 (.out(clock_3_out));
  Clock #(.highDuration(16), .lowDuration(16)) clock_4 (.out(clock_4_out));
  Clock #(.highDuration(32), .lowDuration(6)) clock_5 (.out(clock_5_out));
  Clock #(.highDuration(2), .lowDuration(2)) clock_6 (.out(clock_6_out));
  Clock clock_7 (.out(clock_7_out));
  Clock #(.highDuration(4), .lowDuration(2)) clock_8 (.out(clock_8_out));
endmodule
