// Logisim project Extra 01.circ as structural Verilog: 1 circuit, main circuit main
module main (
  input  a,
  input  b,
  input  c,
  input  d,
  input  e,
  input  f,
  output out_7
);

  wire nor_1_out, nor_2_out, nor_3_out;

  nor nor_1 (nor_1_out, a, b);
  nor nor_2 (nor_2_out, c, d);
  nor nor_3 (nor_3_out, e, f);
  and and_1 (out_7, nor_1_out, nor_2_out, nor_3_out);

  // Notes on the sheet:
  //   Mateus Augusto Moraes Ferreira    Matricula: 435669
endmodule
