// Logisim project Extra 02.circ as structural Verilog: 1 circuit, main circuit main
module main (
  input  a,
  input  b,
  input  c,
  input  d,
  input  e,
  input  f,
  output s
);

  wire nor_1_out, nor_2_out, nor_3_out;

  nor nor_1 (nor_1_out, a, b);
  nor nor_2 (nor_2_out, c, d);
  nor nor_3 (nor_3_out, e, f);
  nand nand_1 (s, nor_1_out, nor_2_out, nor_3_out);

  // Notes on the sheet:
  //   Mateus Augusto Moraes Ferreira     Matricula: 435669
endmodule
