// Logisim project Extra01.circ as structural Verilog: 1 circuit, main circuit main
module main (
  input  a,
  input  b,
  input  in_3,
  input  in_4,
  output out_5
);

  wire nor_1_out, nor_2_out;

  nor nor_1 (nor_1_out, a, b);
  nor nor_2 (nor_2_out, in_3, in_4);
  and and_1 (out_5, nor_1_out, nor_2_out);

  // Notes on the sheet:
  //   438964 - Ederson Cristiano Nunes
endmodule
