// Logisim project Extra02.circ as structural Verilog: 1 circuit, main circuit main
module main (
  input  _1,
  input  _2,
  input  _3,
  input  _4,
  output s
);

  wire nor_1_out, nor_2_out;

  nor nor_1 (nor_1_out, _1, _2);
  nor nor_2 (nor_2_out, _3, _4);
  and and_1 (s, nor_1_out, nor_2_out);

  // Notes on the sheet:
  //   438964 - Ederson Cristiano Nunes
endmodule
