// Logisim project C2.circ as structural Verilog: 2 circuits, main circuit main
module main (
  input  [7:0] Entrada_de_byte,
  output [7:0] out_2
);

  wire adder_1_cout;
  wire [7:0] c1_1_out_2;

  C1 c1_1 (.in_1(Entrada_de_byte), .out_2(c1_1_out_2));
  // Probe on {8{1'b0}}
  Adder adder_1 (.a(c1_1_out_2), .b({8{1'b0}}), .out(out_2), .cin(1'b1), .cout(adder_1_cout));
  // Probe on adder_1_cout

  // Notes on the sheet:
  //   mais 1
  //   Resposta complemento de 2
endmodule

module C1 (
  input  [7:0] in_1,
  output [7:0] out_2
);

  assign out_2 = ~in_1;  // NOT_Gate not_1, 8 bits wide
endmodule
