// Logisim project Extra01.circ as structural Verilog: 1 circuit, main circuit main
module main (
  input  [7:0] a,
  output [7:0] b
);

  assign b = ~a;  // NOT_Gate not_1, 8 bits wide

  // Notes on the sheet:
  //   Mateus Augusto Moraes Ferreira     Matricula:435669
endmodule
