// Logisim project Guia3.circ as structural Verilog: 8 circuits, main circuit LUandSor
module LUandSor (
  input  \OPÇÃO ,
  input  A0,
  input  A1,
  input  A2,
  input  A3,
  input  B0,
  input  B1,
  input  B2,
  input  B3,
  output O0,
  output O1,
  output O2,
  output O3
);

  wire and_1_out, and_2_out, and_3_out, and_4_out, or_1_out, or_2_out, or_3_out, or_4_out;

  and and_1 (and_1_out, B0, A0);
  and and_2 (and_2_out, B1, A1);
  and and_3 (and_3_out, B2, A2);
  and and_4 (and_4_out, B3, A3);
  or or_1 (or_1_out, A0, B0);
  or or_2 (or_2_out, A1, B1);
  or or_3 (or_3_out, A2, B2);
  or or_4 (or_4_out, A3, B3);
  Optador4B optador4b_1 (
    .\Opção (\OPÇÃO ), .A0(and_1_out), .A1(and_2_out), .A2(and_3_out), .A3(and_4_out), .B0(or_1_out),
    .B1(or_2_out), .B2(or_3_out), .B3(or_4_out), .O0(O0), .O1(O1), .O2(O2), .O3(O3));
endmodule

module Optador1B (
  input  B,
  input  A,
  input  \Opção ,
  output Out
);

  wire and_1_out, and_2_out, not_1_out;

  and and_1 (and_1_out, B, \Opção );
  and and_2 (and_2_out, A, not_1_out);
  not not_1 (not_1_out, \Opção );
  or or_1 (Out, and_1_out, and_2_out);
endmodule

module Optador4B (
  input  \Opção ,
  input  A0,
  input  A1,
  input  A2,
  input  A3,
  input  B0,
  input  B1,
  input  B2,
  input  B3,
  output O0,
  output O1,
  output O2,
  output O3
);

  Optador1B optador1b_1 (.B(B0), .A(A0), .\Opção (\Opção ), .Out(O0));
  Optador1B optador1b_2 (.B(B1), .A(A1), .\Opção (\Opção ), .Out(O1));
  Optador1B optador1b_3 (.B(B2), .A(A2), .\Opção (\Opção ), .Out(O2));
  Optador1B optador1b_4 (.B(B3), .A(A3), .\Opção (\Opção ), .Out(O3));
endmodule

module LUandOr (
  input  A0,
  input  A1,
  input  A2,
  input  A3,
  input  B0,
  input  B1,
  input  B2,
  input  B3,
  output E0,
  output E1,
  output E2,
  output E3,
  output O0,
  output O1,
  output O2,
  output O3
);

  and and_1 (E0, B0, A0);
  and and_2 (E1, B1, A1);
  and and_3 (E2, B2, A2);
  and and_4 (E3, B3, A3);
  or or_1 (O0, A0, B0);
  or or_2 (O1, A1, B1);
  or or_3 (O2, A2, B2);
  or or_4 (O3, A3, B3);
endmodule

module LUandOrSnandNor (
  input  \Opção ,
  input  A0,
  input  A1,
  input  A2,
  input  A3,
  input  B0,
  input  B1,
  input  B2,
  input  B3,
  output O0,
  output O1,
  output O2,
  output O3,
  output O4,
  output O5,
  output O6,
  output O7
);

  wire and_1_out, and_2_out, and_3_out, and_4_out, or_1_out, or_2_out, or_3_out, or_4_out;

  and and_1 (and_1_out, A0, B0);
  and and_2 (and_2_out, A1, B1);
  and and_3 (and_3_out, A2, B2);
  and and_4 (and_4_out, A3, B3);
  or or_1 (or_1_out, B0, A0);
  or or_2 (or_2_out, B1, A1);
  or or_3 (or_3_out, B2, A2);
  or or_4 (or_4_out, B3, A3);
  xor xor_1 (O0, and_1_out, \Opção );
  xor xor_2 (O1, and_2_out, \Opção );
  xor xor_3 (O2, and_3_out, \Opção );
  xor xor_4 (O3, and_4_out, \Opção );
  xor xor_5 (O4, \Opção , or_1_out);
  xor xor_6 (O5, \Opção , or_2_out);
  xor xor_7 (O6, \Opção , or_3_out);
  xor xor_8 (O7, \Opção , or_4_out);
endmodule

module LUorNorSxorXnor (
  input  \Opção ,
  input  A0,
  input  A1,
  input  A2,
  input  A3,
  input  B0,
  input  B1,
  input  B2,
  input  B3,
  output O0,
  output O1,
  output O2,
  output O3,
  output O4,
  output O5,
  output O6,
  output O7
);

  wire or_1_out, or_2_out, or_3_out, or_4_out, xor_1_out, xor_2_out, xor_3_out, xor_4_out;

  or or_1 (or_1_out, A0, B0);
  or or_2 (or_2_out, A1, B1);
  or or_3 (or_3_out, A2, B2);
  or or_4 (or_4_out, A3, B3);
  xor xor_1 (xor_1_out, A0, B0);
  xor xor_2 (xor_2_out, A1, B1);
  xor xor_3 (xor_3_out, A2, B2);
  xor xor_4 (xor_4_out, A3, B3);
  Optador4B optador4b_1 (
    .\Opção (\Opção ), .A0(or_1_out), .A1(or_2_out), .A2(or_3_out), .A3(or_4_out), .B0(xor_1_out),
    .B1(xor_2_out), .B2(xor_3_out), .B3(xor_4_out), .O0(O0), .O1(O1), .O2(O2), .O3(O3));
  not not_1 (O4, O0);
  not not_2 (O5, O1);
  not not_3 (O6, O2);
  not not_4 (O7, O3);
endmodule

module LUnotOrNorAndNandXorXnor (
  input  A,
  input  B,
  output out_3,
  output out_4,
  output out_5,
  output out_6,
  output out_7,
  output out_8,
  output out_9,
  output out_10
);

  not not_1 (out_3, A);
  not not_2 (out_4, B);
  or or_1 (out_5, A, B);
  not not_3 (out_6, out_5);
  and and_1 (out_7, A, B);
  not not_4 (out_8, out_7);
  xor xor_1 (out_9, A, B);
  not not_5 (out_10, out_9);
endmodule

module LUigSdif (
  input  \Opção ,
  input  A0,
  input  A1,
  input  A2,
  input  A3,
  input  B0,
  input  B1,
  input  B2,
  input  B3,
  output Ig_Dif
);

  wire and_1_out, xnor_1_out, xnor_2_out, xnor_3_out, xnor_4_out;

  xnor xnor_1 (xnor_1_out, A0, B0);
  xnor xnor_2 (xnor_2_out, A1, B1);
  xnor xnor_3 (xnor_3_out, A2, B2);
  xnor xnor_4 (xnor_4_out, A3, B3);
  and and_1 (and_1_out, xnor_1_out, xnor_2_out, xnor_3_out, xnor_4_out);
  xor xor_1 (Ig_Dif, \Opção , and_1_out);
endmodule
