// Logisim project exemplo0031.circ as structural Verilog: 3 circuits, main circuit AND e OR
module AND_e_OR (
  input  in_1,
  input  in_2,
  input  in_3,
  input  in_4,
  input  in_5,
  input  in_6,
  input  in_7,
  input  in_8,
  input  AND,
  input  OR,
  output Saida_AND,
  output Saida_AND_2,
  output Saida_AND_3,
  output Saida_AND_4,
  output Saida_OR,
  output Saida_OR_2,
  output Saida_OR_3,
  output Saida_OR_4
);

  AND and_1 (
    .in_2(in_1), .in_3(in_2), .in_4(in_3), .in_5(in_4), .in_6(in_5), .in_7(in_6), .in_8(in_7), .in_9(in_8),
    .in_1(AND), .out_10(Saida_AND), .out_11(Saida_AND_2), .out_12(Saida_AND_3), .out_13(Saida_AND_4));
  OR or_1 (
    .in_2(in_1), .in_3(in_2), .in_4(in_3), .in_5(in_4), .in_6(in_5), .in_7(in_6), .in_8(in_7), .in_9(in_8),
    .in_1(OR), .out_10(Saida_OR), .out_11(Saida_OR_2), .out_12(Saida_OR_3), .out_13(Saida_OR_4));
endmodule

module AND (
  input  in_1,
  input  in_2,
  input  in_3,
  input  in_4,
  input  in_5,
  input  in_6,
  input  in_7,
  input  in_8,
  input  in_9,
  output out_10,
  output out_11,
  output out_12,
  output out_13
);

  wire and_1_out, and_2_out, and_3_out, and_4_out;

  and and_1 (and_1_out, in_2, in_6);
  and and_2 (and_2_out, in_3, in_7);
  and and_3 (and_3_out, in_4, in_8);
  and and_4 (and_4_out, in_5, in_9);
  and and_5 (out_10, and_1_out, in_1);
  and and_6 (out_11, and_2_out, in_1);
  and and_7 (out_12, and_3_out, in_1);
  and and_8 (out_13, in_1, and_4_out);
endmodule

module OR (
  input  in_1,
  input  in_2,
  input  in_3,
  input  in_4,
  input  in_5,
  input  in_6,
  input  in_7,
  input  in_8,
  input  in_9,
  output out_10,
  output out_11,
  output out_12,
  output out_13
);

  wire or_1_out, or_2_out, or_3_out, or_4_out;

  or or_1 (or_1_out, in_2, in_6);
  or or_2 (or_2_out, in_3, in_7);
  or or_3 (or_3_out, in_4, in_8);
  or or_4 (or_4_out, in_5, in_9);
  and and_1 (out_10, or_1_out, in_1);
  and and_2 (out_11, or_2_out, in_1);
  and and_3 (out_12, or_3_out, in_1);
  and and_4 (out_13, in_1, or_4_out);
endmodule
