// Logisim project exemplo0032.circ as structural Verilog: 3 circuits, main circuit OR e AND selecionáveis
module \OR_e_AND_selecionáveis  (
  input  in_1,
  input  in_2,
  input  in_3,
  input  in_4,
  input  in_5,
  input  in_6,
  input  in_7,
  input  in_8,
  input  AND__1___e_OR__0,
  output out_10,
  output out_11,
  output out_12,
  output out_13
);

  wire and_1_out_10, and_1_out_11, and_1_out_12, and_1_out_13, or_1_out_10, or_1_out_11, or_1_out_12,
       or_1_out_13;

  AND and_1 (
    .in_2(in_1), .in_3(in_2), .in_4(in_3), .in_5(in_4), .in_6(in_5), .in_7(in_6), .in_8(in_7), .in_9(in_8),
    .in_1(AND__1___e_OR__0), .out_10(and_1_out_10), .out_11(and_1_out_11), .out_12(and_1_out_12),
    .out_13(and_1_out_13));
  OR or_1 (
    .in_2(in_1), .in_3(in_2), .in_4(in_3), .in_5(in_4), .in_6(in_5), .in_7(in_6), .in_8(in_7), .in_9(in_8),
    .in_1(AND__1___e_OR__0), .out_10(or_1_out_10), .out_11(or_1_out_11), .out_12(or_1_out_12),
    .out_13(or_1_out_13));
  xor xor_1 (out_10, and_1_out_10, or_1_out_10);
  xor xor_2 (out_11, and_1_out_11, or_1_out_11);
  xor xor_3 (out_12, and_1_out_12, or_1_out_12);
  xor xor_4 (out_13, and_1_out_13, or_1_out_13);
endmodule

module OR (
  input  in_1,
  input  in_2,
  input  in_3,
  input  in_4,
  input  in_5,
  input  in_6,
  input  in_7,
  input  in_8,
  input  in_9,
  output out_10,
  output out_11,
  output out_12,
  output out_13
);

  wire not_1_out, not_2_out, not_3_out, not_4_out, or_1_out, or_2_out, or_3_out, or_4_out;

  or or_1 (or_1_out, in_2, in_6);
  or or_2 (or_2_out, in_3, in_7);
  or or_3 (or_3_out, in_4, in_8);
  or or_4 (or_4_out, in_5, in_9);
  not not_1 (not_1_out, in_1);
  not not_2 (not_2_out, in_1);
  not not_3 (not_3_out, in_1);
  not not_4 (not_4_out, in_1);
  and and_1 (out_10, not_1_out, or_1_out);
  and and_2 (out_11, not_2_out, or_2_out);
  and and_3 (out_12, not_3_out, or_3_out);
  and and_4 (out_13, not_4_out, or_4_out);
endmodule

module AND (
  input  in_1,
  input  in_2,
  input  in_3,
  input  in_4,
  input  in_5,
  input  in_6,
  input  in_7,
  input  in_8,
  input  in_9,
  output out_10,
  output out_11,
  output out_12,
  output out_13
);

  wire and_1_out, and_2_out, and_3_out, and_4_out;

  and and_1 (and_1_out, in_2, in_6);
  and and_2 (and_2_out, in_3, in_7);
  and and_3 (and_3_out, in_4, in_8);
  and and_4 (and_4_out, in_5, in_9);
  and and_5 (out_10, in_1, and_1_out);
  and and_6 (out_11, in_1, and_2_out);
  and and_7 (out_12, in_1, and_3_out);
  and and_8 (out_13, in_1, and_4_out);
endmodule
