// Logisim project exemplo0033.circ as structural Verilog: 5 circuits, main circuit OR, NOR, XOR e XNOR
module OR__NOR__XOR_e_XNOR (
  input  in_1,
  input  in_2,
  input  in_3,
  input  in_4,
  input  in_5,
  input  in_6,
  input  in_7,
  input  in_8,
  input  OR__0___e_NOR__1,
  input  XOR__0___e__XNOR__1,
  output out_11,
  output out_12,
  output out_13,
  output out_14,
  output out_15,
  output out_16,
  output out_17,
  output out_18
);

  wire nor_1_out_10, nor_1_out_11, nor_1_out_12, nor_1_out_13, or_1_out_10, or_1_out_11, or_1_out_12,
       or_1_out_13, xnor_1_out_10, xnor_1_out_11, xnor_1_out_12, xnor_1_out_13, xor_1_out_10, xor_1_out_11,
       xor_1_out_12, xor_1_out_13;

  OR or_1 (
    .in_2(in_1), .in_3(in_2), .in_4(in_3), .in_5(in_4), .in_6(in_5), .in_7(in_6), .in_8(in_7), .in_9(in_8),
    .in_1(OR__0___e_NOR__1), .out_10(or_1_out_10), .out_11(or_1_out_11), .out_12(or_1_out_12),
    .out_13(or_1_out_13));
  NOR nor_1 (
    .in_2(in_1), .in_3(in_2), .in_4(in_3), .in_5(in_4), .in_6(in_5), .in_7(in_6), .in_8(in_7), .in_9(in_8),
    .in_1(OR__0___e_NOR__1), .out_10(nor_1_out_10), .out_11(nor_1_out_11), .out_12(nor_1_out_12),
    .out_13(nor_1_out_13));
  XOR xor_1 (
    .in_2(in_1), .in_3(in_2), .in_4(in_3), .in_5(in_4), .in_6(in_5), .in_7(in_6), .in_8(in_7), .in_9(in_8),
    .in_1(XOR__0___e__XNOR__1), .out_10(xor_1_out_10), .out_11(xor_1_out_11), .out_12(xor_1_out_12),
    .out_13(xor_1_out_13));
  XNOR xnor_1 (
    .in_2(in_1), .in_3(in_2), .in_4(in_3), .in_5(in_4), .in_6(in_5), .in_7(in_6), .in_8(in_7), .in_9(in_8),
    .in_1(XOR__0___e__XNOR__1), .out_10(xnor_1_out_10), .out_11(xnor_1_out_11), .out_12(xnor_1_out_12),
    .out_13(xnor_1_out_13));
  xor xor_2 (out_11, or_1_out_10, nor_1_out_10);
  xor xor_3 (out_12, or_1_out_11, nor_1_out_11);
  xor xor_4 (out_13, or_1_out_12, nor_1_out_12);
  xor xor_5 (out_14, or_1_out_13, nor_1_out_13);
  xor xor_6 (out_15, xor_1_out_10, xnor_1_out_10);
  xor xor_7 (out_16, xor_1_out_11, xnor_1_out_11);
  xor xor_8 (out_17, xor_1_out_12, xnor_1_out_12);
  xor xor_9 (out_18, xor_1_out_13, xnor_1_out_13);
endmodule

module OR (
  input  in_1,
  input  in_2,
  input  in_3,
  input  in_4,
  input  in_5,
  input  in_6,
  input  in_7,
  input  in_8,
  input  in_9,
  output out_10,
  output out_11,
  output out_12,
  output out_13
);

  wire not_1_out, not_2_out, not_3_out, not_4_out, or_1_out, or_2_out, or_3_out, or_4_out;

  or or_1 (or_1_out, in_2, in_6);
  or or_2 (or_2_out, in_3, in_7);
  or or_3 (or_3_out, in_4, in_8);
  or or_4 (or_4_out, in_5, in_9);
  not not_1 (not_1_out, in_1);
  not not_2 (not_2_out, in_1);
  not not_3 (not_3_out, in_1);
  not not_4 (not_4_out, in_1);
  and and_1 (out_10, or_1_out, not_1_out);
  and and_2 (out_11, or_2_out, not_2_out);
  and and_3 (out_12, or_3_out, not_3_out);
  and and_4 (out_13, or_4_out, not_4_out);
endmodule

module NOR (
  input  in_1,
  input  in_2,
  input  in_3,
  input  in_4,
  input  in_5,
  input  in_6,
  input  in_7,
  input  in_8,
  input  in_9,
  output out_10,
  output out_11,
  output out_12,
  output out_13
);

  wire nor_1_out, nor_2_out, nor_3_out, nor_4_out;

  nor nor_1 (nor_1_out, in_2, in_6);
  nor nor_2 (nor_2_out, in_3, in_7);
  nor nor_3 (nor_3_out, in_4, in_8);
  nor nor_4 (nor_4_out, in_5, in_9);
  and and_1 (out_10, nor_1_out, in_1);
  and and_2 (out_11, nor_2_out, in_1);
  and and_3 (out_12, nor_3_out, in_1);
  and and_4 (out_13, nor_4_out, in_1);
endmodule

module XNOR (
  input  in_1,
  input  in_2,
  input  in_3,
  input  in_4,
  input  in_5,
  input  in_6,
  input  in_7,
  input  in_8,
  input  in_9,
  output out_10,
  output out_11,
  output out_12,
  output out_13
);

  wire xnor_1_out, xnor_2_out, xnor_3_out, xnor_4_out;

  xnor xnor_1 (xnor_1_out, in_2, in_6);
  xnor xnor_2 (xnor_2_out, in_3, in_7);
  xnor xnor_3 (xnor_3_out, in_4, in_8);
  xnor xnor_4 (xnor_4_out, in_5, in_9);
  and and_1 (out_10, xnor_1_out, in_1);
  and and_2 (out_11, xnor_2_out, in_1);
  and and_3 (out_12, xnor_3_out, in_1);
  and and_4 (out_13, xnor_4_out, in_1);
endmodule

module XOR (
  input  in_1,
  input  in_2,
  input  in_3,
  input  in_4,
  input  in_5,
  input  in_6,
  input  in_7,
  input  in_8,
  input  in_9,
  output out_10,
  output out_11,
  output out_12,
  output out_13
);

  wire not_1_out, not_2_out, not_3_out, not_4_out, xor_1_out, xor_2_out, xor_3_out, xor_4_out;

  xor xor_1 (xor_1_out, in_2, in_6);
  xor xor_2 (xor_2_out, in_3, in_7);
  xor xor_3 (xor_3_out, in_4, in_8);
  xor xor_4 (xor_4_out, in_5, in_9);
  not not_1 (not_1_out, in_1);
  not not_2 (not_2_out, in_1);
  not not_3 (not_3_out, in_1);
  not not_4 (not_4_out, in_1);
  and and_1 (out_10, xor_1_out, not_1_out);
  and and_2 (out_11, xor_2_out, not_2_out);
  and and_3 (out_12, xor_3_out, not_3_out);
  and and_4 (out_13, xor_4_out, not_4_out);
endmodule
