// Logisim project exemplo0034.circ as structural Verilog: 5 circuits, main circuit AND, NAND, OR e NOR
module AND__NAND__OR_e_NOR (
  input  in_1,
  input  in_2,
  input  in_3,
  input  in_4,
  input  in_5,
  input  in_6,
  input  in_7,
  input  in_8,
  input  AND__1___e_NAND__0,
  input  OR__1___e_NOR__0,
  output out_11,
  output out_12,
  output out_13,
  output out_14,
  output out_15,
  output out_16,
  output out_17,
  output out_18
);

  wire and_1_out_10, and_1_out_11, and_1_out_12, and_1_out_13, nand_1_out_10, nand_1_out_11, nand_1_out_12,
       nand_1_out_13, nor_1_out_10, nor_1_out_11, nor_1_out_12, nor_1_out_13, or_1_out_10, or_1_out_11,
       or_1_out_12, or_1_out_13;

  AND and_1 (
    .in_2(in_1), .in_3(in_2), .in_4(in_3), .in_5(in_4), .in_6(in_5), .in_7(in_6), .in_8(in_7), .in_9(in_8),
    .in_1(AND__1___e_NAND__0), .out_10(and_1_out_10), .out_11(and_1_out_11), .out_12(and_1_out_12),
    .out_13(and_1_out_13));
  NAND nand_1 (
    .in_2(in_1), .in_3(in_2), .in_4(in_3), .in_5(in_4), .in_6(in_5), .in_7(in_6), .in_8(in_7), .in_9(in_8),
    .in_1(AND__1___e_NAND__0), .out_10(nand_1_out_10), .out_11(nand_1_out_11), .out_12(nand_1_out_12),
    .out_13(nand_1_out_13));
  OR or_1 (
    .in_2(in_1), .in_3(in_2), .in_4(in_3), .in_5(in_4), .in_6(in_5), .in_7(in_6), .in_8(in_7), .in_9(in_8),
    .in_1(OR__1___e_NOR__0), .out_10(or_1_out_10), .out_11(or_1_out_11), .out_12(or_1_out_12),
    .out_13(or_1_out_13));
  NOR nor_1 (
    .in_2(in_1), .in_3(in_2), .in_4(in_3), .in_5(in_4), .in_6(in_5), .in_7(in_6), .in_8(in_7), .in_9(in_8),
    .in_1(OR__1___e_NOR__0), .out_10(nor_1_out_10), .out_11(nor_1_out_11), .out_12(nor_1_out_12),
    .out_13(nor_1_out_13));
  xor xor_1 (out_11, and_1_out_10, nand_1_out_10);
  xor xor_2 (out_12, and_1_out_11, nand_1_out_11);
  xor xor_3 (out_13, and_1_out_12, nand_1_out_12);
  xor xor_4 (out_14, and_1_out_13, nand_1_out_13);
  xor xor_5 (out_15, or_1_out_10, nor_1_out_10);
  xor xor_6 (out_16, or_1_out_11, nor_1_out_11);
  xor xor_7 (out_17, or_1_out_12, nor_1_out_12);
  xor xor_8 (out_18, or_1_out_13, nor_1_out_13);
endmodule

module AND (
  input  in_1,
  input  in_2,
  input  in_3,
  input  in_4,
  input  in_5,
  input  in_6,
  input  in_7,
  input  in_8,
  input  in_9,
  output out_10,
  output out_11,
  output out_12,
  output out_13
);

  wire and_1_out, and_2_out, and_3_out, and_4_out;

  and and_1 (and_1_out, in_2, in_6);
  and and_2 (and_2_out, in_3, in_7);
  and and_3 (and_3_out, in_4, in_8);
  and and_4 (and_4_out, in_5, in_9);
  and and_5 (out_10, and_1_out, in_1);
  and and_6 (out_11, and_2_out, in_1);
  and and_7 (out_12, and_3_out, in_1);
  and and_8 (out_13, and_4_out, in_1);
endmodule

module NAND (
  input  in_1,
  input  in_2,
  input  in_3,
  input  in_4,
  input  in_5,
  input  in_6,
  input  in_7,
  input  in_8,
  input  in_9,
  output out_10,
  output out_11,
  output out_12,
  output out_13
);

  wire nand_1_out, nand_2_out, nand_3_out, nand_4_out, not_1_out, not_2_out, not_3_out, not_4_out;

  nand nand_1 (nand_1_out, in_2, in_6);
  nand nand_2 (nand_2_out, in_3, in_7);
  nand nand_3 (nand_3_out, in_4, in_8);
  nand nand_4 (nand_4_out, in_5, in_9);
  not not_1 (not_1_out, in_1);
  not not_2 (not_2_out, in_1);
  not not_3 (not_3_out, in_1);
  not not_4 (not_4_out, in_1);
  and and_1 (out_10, nand_1_out, not_1_out);
  and and_2 (out_11, nand_2_out, not_2_out);
  and and_3 (out_12, nand_3_out, not_3_out);
  and and_4 (out_13, nand_4_out, not_4_out);
endmodule

module OR (
  input  in_1,
  input  in_2,
  input  in_3,
  input  in_4,
  input  in_5,
  input  in_6,
  input  in_7,
  input  in_8,
  input  in_9,
  output out_10,
  output out_11,
  output out_12,
  output out_13
);

  wire or_1_out, or_2_out, or_3_out, or_4_out;

  or or_1 (or_1_out, in_2, in_6);
  or or_2 (or_2_out, in_3, in_7);
  or or_3 (or_3_out, in_4, in_8);
  or or_4 (or_4_out, in_5, in_9);
  and and_1 (out_10, or_1_out, in_1);
  and and_2 (out_11, or_2_out, in_1);
  and and_3 (out_12, or_3_out, in_1);
  and and_4 (out_13, or_4_out, in_1);
endmodule

module NOR (
  input  in_1,
  input  in_2,
  input  in_3,
  input  in_4,
  input  in_5,
  input  in_6,
  input  in_7,
  input  in_8,
  input  in_9,
  output out_10,
  output out_11,
  output out_12,
  output out_13
);

  wire nor_1_out, nor_2_out, nor_3_out, nor_4_out, not_1_out, not_2_out, not_3_out, not_4_out;

  nor nor_1 (nor_1_out, in_2, in_6);
  nor nor_2 (nor_2_out, in_3, in_7);
  nor nor_3 (nor_3_out, in_4, in_8);
  nor nor_4 (nor_4_out, in_5, in_9);
  not not_1 (not_1_out, in_1);
  not not_2 (not_2_out, in_1);
  not not_3 (not_3_out, in_1);
  not not_4 (not_4_out, in_1);
  and and_1 (out_10, nor_1_out, not_1_out);
  and and_2 (out_11, nor_2_out, not_2_out);
  and and_3 (out_12, nor_3_out, not_3_out);
  and and_4 (out_13, nor_4_out, not_4_out);
endmodule
