// Logisim project guai03.circ as structural Verilog
module Exercicio0031 (
  input  [3:0] P,
  input  [3:0] Q,
  output [3:0] S_3_0,
  output [3:0] S_7_4
);

  assign S_3_0 = Q & P;  // AND_Gate and_1, 4 bits wide
  assign S_7_4 = Q | P;  // OR_Gate or_1, 4 bits wide

  // Notes on the sheet:
  //   A saida do Exercicio0031 seria para ser uma unica saida de 8bits onde: o 4 primeiros bits se refenm a saida da AND e os 4 ultima da saido da OR
endmodule

module Exercicio0032 (
  input  A_3,
  input  A_2,
  input  A_1,
  input  A_0,
  input  B_3,
  input  B_2,
  input  B_1,
  input  B_0,
  input  Chave,
  output S0,
  output S1,
  output S2,
  output S3
);

  wire AND0_out, AND1_out, AND2_out, AND3_out, and_1_out, and_2_out, and_3_out, and_4_out, and_5_out,
       and_6_out, and_7_out, and_8_out, not_1_out, OR0_out, OR1_out, OR2_out, OR3_out;

  and AND0 (AND0_out, A_0, B_0);
  or OR0 (OR0_out, A_0, B_0);
  and AND1 (AND1_out, A_1, B_1);
  or OR1 (OR1_out, A_1, B_1);
  and AND2 (AND2_out, A_2, B_2);
  or OR2 (OR2_out, A_2, B_2);
  and AND3 (AND3_out, A_3, B_3);
  or OR3 (OR3_out, A_3, B_3);
  and and_1 (and_1_out, AND3_out, Chave);
  and and_2 (and_2_out, OR3_out, not_1_out);
  not not_1 (not_1_out, Chave);
  and and_3 (and_3_out, AND0_out, Chave);
  or or_1 (S0, and_3_out, and_4_out);
  and and_4 (and_4_out, OR0_out, not_1_out);
  and and_5 (and_5_out, AND1_out, Chave);
  or or_2 (S1, and_5_out, and_6_out);
  and and_6 (and_6_out, OR1_out, not_1_out);
  and and_7 (and_7_out, AND2_out, Chave);
  or or_3 (S2, and_7_out, and_8_out);
  and and_8 (and_8_out, OR2_out, not_1_out);
  or or_4 (S3, and_1_out, and_2_out);

  // Notes on the sheet:
  //   Entrada A
  //   Entrada B
  //    0 - OR
  //   1 - AND
endmodule

// AND
module AND_4bits (
  input  A_3,
  input  A_2,
  input  A_1,
  input  A_0,
  input  B_3,
  input  B_2,
  input  B_1,
  input  B_0,
  output S0,
  output S1,
  output S2,
  output S3
);

  and and_1 (S0, B_0, A_0);
  and and_2 (S1, B_1, A_1);
  and and_3 (S2, B_2, A_2);
  and and_4 (S3, B_3, A_3);
endmodule

// OR
module OR_4bits (
  input  A_3,
  input  A_2,
  input  A_1,
  input  A_0,
  input  B_3,
  input  B_2,
  input  B_1,
  input  B_0,
  output S0,
  output S1,
  output S2,
  output S3
);

  or or_1 (S0, B_0, A_0);
  or or_2 (S1, B_1, A_1);
  or or_3 (S2, B_2, A_2);
  or or_4 (S3, B_3, A_3);
endmodule

module Exercicio0033 (
  input  Chave,
  input  A_3,
  input  A_2,
  input  A_1,
  input  A_0,
  input  B_3,
  input  B_2,
  input  B_1,
  input  B_0,
  output S4,
  output S0,
  output S5,
  output S1,
  output S6,
  output S2,
  output S7,
  output S3
);

  wire and_4bits_1_s0, and_4bits_1_s1, and_4bits_1_s2, and_4bits_1_s3, or_4bits_1_s0, or_4bits_1_s1,
       or_4bits_1_s2, or_4bits_1_s3;

  not not_1 (S4, S0);
  choice u_S0 (.KEY(Chave), .A(and_4bits_1_s0), .B(or_4bits_1_s0), .S(S0));
  not not_2 (S5, S1);
  OR_4bits or_4bits_1 (
    .A_3(A_3), .A_2(A_2), .A_1(A_1), .A_0(A_0), .B_3(B_3), .B_2(B_2), .B_1(B_1), .B_0(B_0),
    .S0(or_4bits_1_s0), .S1(or_4bits_1_s1), .S2(or_4bits_1_s2), .S3(or_4bits_1_s3));
  AND_4bits and_4bits_1 (
    .A_3(A_3), .A_2(A_2), .A_1(A_1), .A_0(A_0), .B_3(B_3), .B_2(B_2), .B_1(B_1), .B_0(B_0),
    .S0(and_4bits_1_s0), .S1(and_4bits_1_s1), .S2(and_4bits_1_s2), .S3(and_4bits_1_s3));
  choice u_S1 (.KEY(Chave), .A(and_4bits_1_s1), .B(or_4bits_1_s1), .S(S1));
  not not_3 (S6, S2);
  choice u_S2 (.KEY(Chave), .A(and_4bits_1_s2), .B(or_4bits_1_s2), .S(S2));
  not not_4 (S7, S3);
  choice u_S3 (.KEY(Chave), .A(and_4bits_1_s3), .B(or_4bits_1_s3), .S(S3));

  // Notes on the sheet:
  //   Entrada A
  //   Entrada B
  //    0 - OR / NOR
  //   1 - AND / NAND
endmodule

module choice (
  input  A,
  input  B,
  input  KEY,
  output S
);

  wire and_1_out, and_2_out, not_1_out;

  not not_1 (not_1_out, KEY);
  and and_1 (and_1_out, B, not_1_out);
  and and_2 (and_2_out, KEY, A);
  or or_1 (S, and_1_out, and_2_out);
endmodule

// XOR
module XOR_4bits (
  input  A_3,
  input  A_2,
  input  A_1,
  input  A_0,
  input  B_3,
  input  B_2,
  input  B_1,
  input  B_0,
  output S0,
  output S1,
  output S2,
  output S3
);

  xor xor_1 (S0, B_0, A_0);
  xor xor_2 (S1, B_1, A_1);
  xor xor_3 (S2, B_2, A_2);
  xor xor_4 (S3, B_3, A_3);
endmodule

module Exercicio0034 (
  input  Chave,
  input  A_3,
  input  A_2,
  input  A_1,
  input  A_0,
  input  B_3,
  input  B_2,
  input  B_1,
  input  B_0,
  output S4,
  output S0,
  output S5,
  output S1,
  output S6,
  output S2,
  output S7,
  output S3
);

  wire or_4bits_1_s0, or_4bits_1_s1, or_4bits_1_s2, or_4bits_1_s3, xor_4bits_1_s0, xor_4bits_1_s1,
       xor_4bits_1_s2, xor_4bits_1_s3;

  not not_1 (S4, S0);
  choice u_S0 (.KEY(Chave), .A(xor_4bits_1_s0), .B(or_4bits_1_s0), .S(S0));
  not not_2 (S5, S1);
  OR_4bits or_4bits_1 (
    .A_3(A_3), .A_2(A_2), .A_1(A_1), .A_0(A_0), .B_3(B_3), .B_2(B_2), .B_1(B_1), .B_0(B_0),
    .S0(or_4bits_1_s0), .S1(or_4bits_1_s1), .S2(or_4bits_1_s2), .S3(or_4bits_1_s3));
  XOR_4bits xor_4bits_1 (
    .A_3(A_3), .A_2(A_2), .A_1(A_1), .A_0(A_0), .B_3(B_3), .B_2(B_2), .B_1(B_1), .B_0(B_0),
    .S0(xor_4bits_1_s0), .S1(xor_4bits_1_s1), .S2(xor_4bits_1_s2), .S3(xor_4bits_1_s3));
  choice u_S1 (.KEY(Chave), .A(xor_4bits_1_s1), .B(or_4bits_1_s1), .S(S1));
  not not_3 (S6, S2);
  choice u_S2 (.KEY(Chave), .A(xor_4bits_1_s2), .B(or_4bits_1_s2), .S(S2));
  not not_4 (S7, S3);
  choice u_S3 (.KEY(Chave), .A(xor_4bits_1_s3), .B(or_4bits_1_s3), .S(S3));

  // Notes on the sheet:
  //   Entrada A
  //   Entrada B
  //    0 - OR / NOR
  //   1 - XOR / XNOR
endmodule

module Exercicio0035 (
  input  A_3,
  input  A_2,
  input  A_1,
  input  A_0,
  input  B_3,
  input  B_2,
  input  B_1,
  input  B_0,
  output S3,
  output S2,
  output S1,
  output S0,
  output S7,
  output S6,
  output S5,
  output S4,
  output S3_2,
  output S2_2,
  output S1_2,
  output S0_2,
  output S7_2,
  output S6_2,
  output S5_2,
  output S4_2,
  output S3_3,
  output S2_3,
  output S1_3,
  output S0_3,
  output S7_3,
  output S6_3,
  output S5_3,
  output S4_3
);

  not not_1 (S7, S3);
  not not_2 (S7_2, S3_2);
  not not_3 (S7_3, S3_3);
  OR_4bits or_4bits_1 (
    .A_3(A_3), .A_2(A_2), .A_1(A_1), .A_0(A_0), .B_3(B_3), .B_2(B_2), .B_1(B_1), .B_0(B_0), .S0(S0), .S1(S1),
    .S2(S2), .S3(S3));
  not not_4 (S6, S2);
  AND_4bits and_4bits_1 (
    .A_3(A_3), .A_2(A_2), .A_1(A_1), .A_0(A_0), .B_3(B_3), .B_2(B_2), .B_1(B_1), .B_0(B_0), .S0(S0_2),
    .S1(S1_2), .S2(S2_2), .S3(S3_2));
  not not_5 (S6_2, S2_2);
  XOR_4bits xor_4bits_1 (
    .A_3(A_3), .A_2(A_2), .A_1(A_1), .A_0(A_0), .B_3(B_3), .B_2(B_2), .B_1(B_1), .B_0(B_0), .S0(S0_3),
    .S1(S1_3), .S2(S2_3), .S3(S3_3));
  not not_6 (S6_3, S2_3);
  not not_7 (S5, S1);
  not not_8 (S5_2, S1_2);
  not not_9 (S5_3, S1_3);
  not not_10 (S4, S0);
  not not_11 (S4_2, S0_2);
  not not_12 (S4_3, S0_3);

  // Notes on the sheet:
  //   OR
  //   NOR
  //   AND
  //   NAND
  //   XOR
  //   XNOR
  //   Entrada A
  //   Entrada B
endmodule
