// Logisim project Exemplo0032.v.circ as structural Verilog: 1 circuit, main circuit main
module main (
  input  [3:0] a,
  input  [3:0] b,
  input  [3:0] _0___Or___1___And,
  output [3:0] out_4
);

  wire [3:0] and_1_out, and_2_out, and_3_out, not_1_out, or_1_out;

  assign and_1_out = b & a;  // AND_Gate and_1, 4 bits wide
  assign or_1_out = a | b;  // OR_Gate or_1, 4 bits wide
  assign not_1_out = ~_0___Or___1___And;  // NOT_Gate not_1, 4 bits wide
  assign and_2_out = and_1_out & _0___Or___1___And;  // AND_Gate and_2, 4 bits wide
  assign and_3_out = or_1_out & not_1_out;  // AND_Gate and_3, 4 bits wide
  assign out_4 = and_2_out | and_3_out;  // OR_Gate or_2, 4 bits wide
endmodule
