// Logisim project Exemplo0033.v.circ as structural Verilog: 3 circuits, main circuit main
module main (
  input  [3:0] a,
  input  [3:0] b,
  input  [3:0] chave,
  output [3:0] And_Nand,
  output [3:0] Or_Nor
);

  wire [3:0] And_Or_and, And_Or_or, Nand_NOr_nand, Nand_NOr_nor, not_1_out, s5_out, s6_out, s7_out, s8_out;

  And_OR And_Or (.a(a), .b(b), .\and (And_Or_and), .\or (And_Or_or));
  NOR__NAND Nand_NOr (.a(a), .b(b), .\nand (Nand_NOr_nand), .\nor (Nand_NOr_nor));
  assign not_1_out = ~chave;  // NOT_Gate not_1, 4 bits wide
  assign s5_out = And_Or_and & not_1_out;  // AND_Gate s5, 4 bits wide
  assign s6_out = And_Or_or & not_1_out;  // AND_Gate s6, 4 bits wide
  assign s7_out = Nand_NOr_nand & chave;  // AND_Gate s7, 4 bits wide
  assign s8_out = Nand_NOr_nor & chave;  // AND_Gate s8, 4 bits wide
  assign And_Nand = s5_out | s7_out;  // OR_Gate s9, 4 bits wide
  assign Or_Nor = s6_out | s8_out;  // OR_Gate s10, 4 bits wide
endmodule

module And_OR (
  input  [3:0] a,
  input  [3:0] b,
  output [3:0] \and ,
  output [3:0] \or 
);

  assign \and  = a & b;  // AND_Gate s1, 4 bits wide
  assign \or  = b | a;  // OR_Gate s2, 4 bits wide
endmodule

module NOR__NAND (
  input  [3:0] a,
  input  [3:0] b,
  output [3:0] \nand ,
  output [3:0] \nor 
);

  assign \nand  = ~(a & b);  // NAND_Gate s3, 4 bits wide
  assign \nor  = ~(a | b);  // NOR_Gate s4, 4 bits wide
endmodule
