// Logisim project Exemplo0034.v.circ as structural Verilog: 5 circuits, main circuit main
module main (
  input  [3:0] a,
  input  [3:0] b,
  input  [3:0] chave,
  output [3:0] Or_Xor,
  output [3:0] Nor_Xnor
);

  wire [3:0] not_1_out, Or_Nor_nor, Or_Nor_or, s5_out, s6_out, s7_out, s8_out, Xor_Xnor_xnor, Xor_Xnor_xor;

  Or_Nor Or_Nor (.a(a), .b(b), .Or(Or_Nor_or), .Nor(Or_Nor_nor));
  Xor_Xnor Xor_Xnor (.a(b), .b(a), .Xor(Xor_Xnor_xor), .Xnor(Xor_Xnor_xnor));
  assign not_1_out = ~chave;  // NOT_Gate not_1, 4 bits wide
  assign s5_out = Or_Nor_or & not_1_out;  // AND_Gate s5, 4 bits wide
  assign s6_out = Or_Nor_nor & not_1_out;  // AND_Gate s6, 4 bits wide
  assign s7_out = Xor_Xnor_xor & chave;  // AND_Gate s7, 4 bits wide
  assign s8_out = Xor_Xnor_xnor & chave;  // AND_Gate s8, 4 bits wide
  assign Or_Xor = s5_out | s7_out;  // OR_Gate s9, 4 bits wide
  assign Nor_Xnor = s6_out | s8_out;  // OR_Gate s10, 4 bits wide
endmodule

module And_OR (
  input  [3:0] a,
  input  [3:0] b,
  output [3:0] \and ,
  output [3:0] \or 
);

  assign \and  = a & b;  // AND_Gate and_1, 4 bits wide
  assign \or  = b | a;  // OR_Gate or_1, 4 bits wide
endmodule

module NOR__NAND (
  input  [3:0] a,
  input  [3:0] b,
  output [3:0] \nand ,
  output [3:0] \nor 
);

  assign \nand  = ~(a & b);  // NAND_Gate nand_1, 4 bits wide
  assign \nor  = ~(a | b);  // NOR_Gate nor_1, 4 bits wide
endmodule

module Xor_Xnor (
  input  [3:0] a,
  input  [3:0] b,
  output [3:0] Xor,
  output [3:0] Xnor
);

  assign Xor = a ^ b;  // XOR_Gate s3, 4 bits wide
  assign Xnor = ~(a ^ b);  // XNOR_Gate s4, 4 bits wide
endmodule

module Or_Nor (
  input  [3:0] a,
  input  [3:0] b,
  output [3:0] Or,
  output [3:0] Nor
);

  assign Or = a | b;  // OR_Gate s1, 4 bits wide
  assign Nor = ~(b | a);  // NOR_Gate s2, 4 bits wide
endmodule
