// Logisim project Exemplo0035.v.circ as structural Verilog: 5 circuits, main circuit main
module main (
  input  [3:0] a,
  input  [3:0] b,
  output [3:0] And,
  output [3:0] Or,
  output [3:0] Nand,
  output [3:0] Nor,
  output [3:0] Xor,
  output [3:0] Xnor,
  output [3:0] na,
  output [3:0] nb
);

  And_OR And_Or (.a(a), .b(b), .\and (And), .\or (Or));
  NOR__NAND Nor_Nand (.a(a), .b(b), .\nand (Nand), .\nor (Nor));
  Xor_Xnor Xor_Xnor (.a(a), .b(b), .Xor(Xor), .Xnor(Xnor));
  assign na = ~a;  // NOT_Gate not_1, 4 bits wide
  assign nb = ~b;  // NOT_Gate not_2, 4 bits wide
endmodule

module And_OR (
  input  [3:0] a,
  input  [3:0] b,
  output [3:0] \and ,
  output [3:0] \or 
);

  assign \and  = a & b;  // AND_Gate and_1, 4 bits wide
  assign \or  = b | a;  // OR_Gate or_1, 4 bits wide
endmodule

module NOR__NAND (
  input  [3:0] a,
  input  [3:0] b,
  output [3:0] \nand ,
  output [3:0] \nor 
);

  assign \nand  = ~(a & b);  // NAND_Gate nand_1, 4 bits wide
  assign \nor  = ~(a | b);  // NOR_Gate nor_1, 4 bits wide
endmodule

module Xor_Xnor (
  input  [3:0] a,
  input  [3:0] b,
  output [3:0] Xor,
  output [3:0] Xnor
);

  assign Xor = a ^ b;  // XOR_Gate xor_1, 4 bits wide
  assign Xnor = ~(a ^ b);  // XNOR_Gate xnor_1, 4 bits wide
endmodule

module Or_Nor (
  input  [3:0] a,
  input  [3:0] b,
  output [3:0] Or,
  output [3:0] Nor
);

  assign Or = a | b;  // OR_Gate or_1, 4 bits wide
  assign Nor = ~(b | a);  // NOR_Gate nor_1, 4 bits wide
endmodule
