// Logisim project Exemplo0032.circ as structural Verilog: 2 circuits, main circuit main
module main (
  input  [3:0] a,
  input  [3:0] b,
  input  [3:0] c,
  output [3:0] s
);

  wire [3:0] and_1_out, and_2_out, and_3_out, not_1_out, not_2_out;

  assign not_1_out = ~c;  // NOT_Gate not_1, 4 bits wide
  assign not_2_out = ~c;  // NOT_Gate not_2, 4 bits wide
  assign and_1_out = b & not_1_out;  // AND_Gate and_1, 4 bits wide
  assign and_2_out = a & not_2_out;  // AND_Gate and_2, 4 bits wide
  assign s = and_1_out | and_2_out | and_3_out;  // OR_Gate or_1, 4 bits wide
  assign and_3_out = a & b;  // AND_Gate and_3, 4 bits wide

  // Notes on the sheet:
  //   0000 - OR
  //   1111 - AND
  //   Unidade Lógica com operações AND e OR, selecionável para 4 bits
endmodule

module gfr (
  input  [3:0] in_1,
  input  [3:0] in_2,
  output [3:0] out_3,
  output [3:0] out_4
);

  // main main_1: pin names not known; wires that end beside it: in_1, in_2, out_3, out_4
endmodule
