// Logisim project Exemplo0034.circ as structural Verilog: 1 circuit, main circuit main
module main (
  input  [3:0] x,
  input  [3:0] y,
  input  [3:0] chave,
  output [3:0] out_4,
  output [3:0] out_5
);

  wire [3:0] and_1_out, and_2_out, and_3_out, and_4_out, not_1_out, not_2_out, s2_out, s3_out, s4_out, s5_out;

  assign s5_out = x | y;  // OR_Gate s5, 4 bits wide
  assign s2_out = x ^ y;  // XOR_Gate s2, 4 bits wide
  assign s3_out = ~(x | y);  // NOR_Gate s3, 4 bits wide
  assign s4_out = ~(y ^ x);  // XNOR_Gate s4, 4 bits wide
  assign not_1_out = ~chave;  // NOT_Gate not_1, 4 bits wide
  assign not_2_out = ~chave;  // NOT_Gate not_2, 4 bits wide
  assign and_1_out = s5_out & not_1_out;  // AND_Gate and_1, 4 bits wide
  assign and_2_out = s2_out & chave;  // AND_Gate and_2, 4 bits wide
  assign and_3_out = s3_out & not_2_out;  // AND_Gate and_3, 4 bits wide
  assign and_4_out = s4_out & chave;  // AND_Gate and_4, 4 bits wide
  assign out_4 = and_1_out | and_2_out;  // OR_Gate s0, 4 bits wide
  assign out_5 = and_3_out | and_4_out;  // OR_Gate s1, 4 bits wide

  // Notes on the sheet:
  //   0 - OR/NOR
  //   1 - XOR/XNOR
  //   Unidade Lógica com portas XOR e XNOR / OR e NOR, selecionáveis
  //   module cx1
  //   module cx2
endmodule
