// Logisim project Exemplo0031.circ as structural Verilog: 1 circuit, main circuit main
module main (
  input  in_1,
  input  in_2,
  input  in_3,
  input  in_4,
  output out_5,
  output out_6,
  output out_7
);

  and and_1 (out_5, in_1, in_2, in_3, in_4);
  or or_1 (out_7, in_1, in_2, in_4, in_3);
  and and_2 (out_6, out_5, out_7);
endmodule
