// Logisim project Exemplo0032.circ as structural Verilog: 1 circuit, main circuit main
module main (
  input  in_1,
  input  in_2,
  input  in_3,
  input  in_4,
  input  in_5,
  output out_6
);

  wire and_1_out, not_1_out, or_1_out;

  not not_1 (not_1_out, in_5);
  or or_1 (or_1_out, in_1, in_2, in_3, in_4, not_1_out);
  and and_1 (and_1_out, in_2, in_1, in_3, in_4, in_5);
  or or_2 (out_6, or_1_out, and_1_out);
endmodule
