// Logisim project Exemplo0033.circ as structural Verilog: 1 circuit, main circuit main
module main (
  input  in_1,
  input  in_2,
  input  in_3,
  input  in_4,
  input  in_5,
  output out_6,
  output out_7
);

  wire and_1_out, nand_1_out, nor_1_out, not_1_out, or_1_out;

  not not_1 (not_1_out, in_5);
  or or_1 (or_1_out, in_1, in_2, in_3, in_4, not_1_out);
  and and_1 (and_1_out, in_2, in_1, in_3, in_4, not_1_out);
  nor nor_1 (nor_1_out, in_3, in_1, in_2, in_4, in_5);
  nand nand_1 (nand_1_out, in_4, in_1, in_2, in_3, in_5);
  or or_2 (out_6, or_1_out, and_1_out);
  or or_3 (out_7, nor_1_out, nand_1_out);
endmodule
