// Logisim project Exemplo0034.circ as structural Verilog: 1 circuit, main circuit main
module main (
  input  in_1,
  input  in_2,
  input  in_3,
  input  in_4,
  input  in_5,
  output out_6,
  output out_7
);

  wire nor_1_out, not_1_out, or_1_out, xnor_1_out, xor_1_out;

  not not_1 (not_1_out, in_5);
  or or_1 (or_1_out, in_1, in_2, in_3, in_4, not_1_out);
  nor nor_1 (nor_1_out, in_1, in_2, in_3, in_4, not_1_out);
  ExactlyOne xor_1 (.out(xor_1_out), .in0(in_1), .in1(in_2), .in2(in_3), .in3(in_4), .in4(in_5));
  NotExactlyOne xnor_1 (.out(xnor_1_out), .in0(in_1), .in1(in_2), .in2(in_3), .in3(in_4), .in4(in_5));
  or or_2 (out_6, or_1_out, nor_1_out);
  or or_3 (out_7, xor_1_out, xnor_1_out);
endmodule
