// Logisim project Exemplo0035.circ as structural Verilog: 1 circuit, main circuit main
module main (
  input  in_1,
  input  in_2,
  input  in_3,
  input  in_4,
  input  in_5,
  input  in_6,
  output out_7,
  output out_8,
  output out_9,
  output out_10,
  output out_11,
  output out_12,
  output out_13
);

  not not_1 (out_7, in_1);
  buf xor_1 (out_12, in_5);  // XOR_Gate
  not xnor_1 (out_13, in_6);  // XNOR_Gate
  buf or_1 (out_8, in_2);  // OR_Gate
  not nor_1 (out_9, in_3);  // NOR_Gate
  not nand_1 (out_11, in_4);  // NAND_Gate
  and and_1 (out_10, out_7, out_8, out_9, out_11, out_12, out_13);
endmodule
