// Logisim project Ex. 1.circ as structural Verilog: 2 circuits, main circuit main
module main (
  input  [2:0] in_1,
  input  [2:0] in_2,
  output [5:0] out_3
);

  wire [2:0] and_1_out, or_1_out;

  assign and_1_out = in_1 & in_2;  // AND_Gate and_1, 3 bits wide
  // Probe on and_1_out
  assign or_1_out = in_1 | in_2;  // OR_Gate or_1, 3 bits wide
  // Probe on or_1_out
  Incluir incluir_1 (.B(and_1_out), .A(or_1_out), .Saida(out_3));
endmodule

module Incluir (
  input  [2:0] B,
  input  [2:0] A,
  output [5:0] Saida
);

  wire bitselector_1_out, bitselector_2_out, bitselector_3_out;
  wire [3:0] bit_extender_1_out;
  wire [4:0] bit_extender_2_out;

  BitSelector #(.width(3)) bitselector_1 (.in(B), .out(bitselector_1_out), .sel(2'b10));
  BitSelector #(.width(3)) bitselector_2 (.in(B), .out(bitselector_2_out), .sel(2'b00));
  BitSelector #(.width(3)) bitselector_3 (.in(B), .out(bitselector_3_out), .sel(2'b01));
  assign bit_extender_1_out = {{1{bitselector_2_out}}, A};  // Bit_Extender bit_extender_1
  assign bit_extender_2_out = {{1{bitselector_3_out}}, bit_extender_1_out};  // Bit_Extender bit_extender_2
  assign Saida = {{1{bitselector_1_out}}, bit_extender_2_out};  // Bit_Extender bit_extender_3
  // Probe on bit_extender_1_out
  // Probe on bit_extender_2_out
endmodule
