// Logisim project Ex. 2.circ as structural Verilog: 1 circuit, main circuit main
module main (
  input  [2:0] Seleto,
  input  [2:0] Porta_A,
  input  [2:0] Porta_B,
  output [2:0] out_4
);

  wire [2:0] and_1_out, and_2_out, and_3_out, not_1_out, or_1_out;

  assign and_1_out = Porta_A & Porta_B;  // AND_Gate and_1, 3 bits wide
  assign or_1_out = Porta_A | Porta_B;  // OR_Gate or_1, 3 bits wide
  assign and_2_out = and_1_out & Seleto;  // AND_Gate and_2, 3 bits wide
  assign not_1_out = ~Seleto;  // NOT_Gate not_1, 3 bits wide
  assign and_3_out = not_1_out & or_1_out;  // AND_Gate and_3, 3 bits wide
  assign out_4 = and_2_out | and_3_out;  // OR_Gate or_2, 3 bits wide
endmodule
