// Logisim project Ex. 3.circ as structural Verilog: 3 circuits, main circuit main
module main (
  input  [2:0] in_1,
  input  [2:0] in_2,
  input  in_3,
  output [5:0] out_4
);

  wire [2:0] and_1_out, and_2_out, and_3_out, and_4_out, and_5_out, mais_1_out_2, nand_1_out, nor_1_out,
       not_1_out, or_1_out, or_2_out, or_3_out;

  assign and_1_out = in_1 & in_2;  // AND_Gate and_1, 3 bits wide
  assign and_2_out = not_1_out & and_1_out;  // AND_Gate and_2, 3 bits wide
  assign and_3_out = not_1_out & or_2_out;  // AND_Gate and_3, 3 bits wide
  assign or_1_out = and_2_out | and_4_out;  // OR_Gate or_1, 3 bits wide
  // Probe on or_1_out
  assign or_2_out = in_1;  // OR_Gate or_2, 3 bits wide OR_Gate
  assign nand_1_out = ~(in_1 & in_2);  // NAND_Gate nand_1, 3 bits wide
  assign not_1_out = ~mais_1_out_2;  // NOT_Gate not_1, 3 bits wide
  assign and_4_out = nand_1_out & mais_1_out_2;  // AND_Gate and_4, 3 bits wide
  assign or_3_out = and_3_out | and_5_out;  // OR_Gate or_3, 3 bits wide
  Incluir incluir_1 (.B(or_1_out), .A(or_3_out), .Saida(out_4));
  assign nor_1_out = ~(in_1 | in_2);  // NOR_Gate nor_1, 3 bits wide
  assign and_5_out = nor_1_out & mais_1_out_2;  // AND_Gate and_5, 3 bits wide
  // Probe on or_3_out
  mais mais_1 (.in_1(in_3), .out_2(mais_1_out_2));
endmodule

module Incluir (
  input  [2:0] B,
  input  [2:0] A,
  output [5:0] Saida
);

  wire bitselector_1_out, bitselector_2_out, bitselector_3_out;
  wire [3:0] bit_extender_1_out;
  wire [4:0] bit_extender_2_out;

  BitSelector #(.width(3)) bitselector_1 (.in(B), .out(bitselector_1_out), .sel(2'b10));
  BitSelector #(.width(3)) bitselector_2 (.in(B), .out(bitselector_2_out), .sel(2'b00));
  BitSelector #(.width(3)) bitselector_3 (.in(B), .out(bitselector_3_out), .sel(2'b01));
  assign bit_extender_1_out = {{1{bitselector_2_out}}, A};  // Bit_Extender bit_extender_1
  assign bit_extender_2_out = {{1{bitselector_3_out}}, bit_extender_1_out};  // Bit_Extender bit_extender_2
  assign Saida = {{1{bitselector_1_out}}, bit_extender_2_out};  // Bit_Extender bit_extender_3
  // Probe on bit_extender_1_out
  // Probe on bit_extender_2_out
endmodule

module mais (
  input  in_1,
  output [2:0] out_2
);

  assign out_2 = {{2{in_1}}, in_1};  // Bit_Extender bit_extender_1
endmodule
