// Logisim project Ex. 5.circ as structural Verilog: 3 circuits, main circuit main
module main (
  input  in_1,
  input  in_2,
  output [6:0] out_3
);

  wire and_1_out, nand_1_out, nor_1_out, not_1_out, or_1_out, xnor_1_out, xor_1_out;
  wire [1:0] bit_extender_1_out;
  wire [2:0] bit_extender_2_out;
  wire [3:0] bit_extender_3_out;
  wire [4:0] bit_extender_4_out;
  wire [5:0] bit_extender_5_out;

  // Probe on not_1_out
  not not_1 (not_1_out, in_1);
  or or_1 (or_1_out, in_1, in_2);
  // Probe on or_1_out
  // Probe on nor_1_out
  assign bit_extender_1_out = {{1{or_1_out}}, not_1_out};  // Bit_Extender bit_extender_1
  and and_1 (and_1_out, in_1, in_2);
  nor nor_1 (nor_1_out, in_1, in_2);
  // Probe on nand_1_out
  // Probe on and_1_out
  assign bit_extender_2_out = {{1{nor_1_out}}, bit_extender_1_out};  // Bit_Extender bit_extender_2
  assign bit_extender_3_out = {{1{and_1_out}}, bit_extender_2_out};  // Bit_Extender bit_extender_3
  xor xor_1 (xor_1_out, in_1, in_2);
  nand nand_1 (nand_1_out, in_1, in_2);
  // Probe on xnor_1_out
  // Probe on xor_1_out
  assign bit_extender_4_out = {{1{nand_1_out}}, bit_extender_3_out};  // Bit_Extender bit_extender_4
  assign bit_extender_5_out = {{1{xor_1_out}}, bit_extender_4_out};  // Bit_Extender bit_extender_5
  xnor xnor_1 (xnor_1_out, in_1, in_2);
  assign out_3 = {{1{xnor_1_out}}, bit_extender_5_out};  // Bit_Extender bit_extender_6
endmodule

module Incluir (
  input  [2:0] B,
  input  [2:0] A,
  output [5:0] Saida
);

  wire bitselector_1_out, bitselector_2_out, bitselector_3_out;
  wire [3:0] bit_extender_1_out;
  wire [4:0] bit_extender_2_out;

  mais mais_1 ();  // open: in_1, out_2
  BitSelector #(.width(3)) bitselector_1 (.in(B), .out(bitselector_1_out), .sel(2'b10));
  BitSelector #(.width(3)) bitselector_2 (.in(B), .out(bitselector_2_out), .sel(2'b00));
  BitSelector #(.width(3)) bitselector_3 (.in(B), .out(bitselector_3_out), .sel(2'b01));
  assign bit_extender_1_out = {{1{bitselector_2_out}}, A};  // Bit_Extender bit_extender_1
  assign bit_extender_2_out = {{1{bitselector_3_out}}, bit_extender_1_out};  // Bit_Extender bit_extender_2
  assign Saida = {{1{bitselector_1_out}}, bit_extender_2_out};  // Bit_Extender bit_extender_3
  // Probe on bit_extender_1_out
  // Probe on bit_extender_2_out
endmodule

module mais (
  input  in_1,
  output [2:0] out_2
);

  assign out_2 = {{2{in_1}}, in_1};  // Bit_Extender bit_extender_1
endmodule
