// Logisim project Guia3.circ as structural Verilog: 5 circuits, main circuit Exemplo0031
module Exemplo0031 (
  input  [3:0] in_1,
  input  [3:0] in_2,
  output [3:0] s1,
  output [3:0] s2
);

  assign s1 = in_2 & in_1;  // AND_Gate and_1, 4 bits wide
  assign s2 = in_2 | in_1;  // OR_Gate or_1, 4 bits wide
endmodule

module Exemplo0032 (
  input  in_1,
  input  in_2,
  input  in_3,
  input  in_4,
  input  in_5,
  input  in_6,
  input  in_7,
  input  in_8,
  input  in_9,
  output out_10,
  output out_11,
  output out_12,
  output out_13
);

  wire and_1_out, and_2_out, and_3_out, and_4_out, and_5_out, and_6_out, and_7_out, and_8_out, and_9_out,
       and_10_out, and_11_out, and_12_out, not_1_out, or_1_out, or_2_out, or_3_out, or_4_out;

  and and_1 (and_1_out, in_5, in_1);
  and and_2 (and_2_out, in_6, in_2);
  and and_3 (and_3_out, in_3, in_7);
  and and_4 (and_4_out, in_8, in_4);
  or or_1 (or_1_out, in_1, in_5);
  or or_2 (or_2_out, in_2, in_6);
  or or_3 (or_3_out, in_3, in_7);
  or or_4 (or_4_out, in_4, in_8);
  not not_1 (not_1_out, in_9);
  and and_5 (and_5_out, and_1_out, in_9);
  and and_6 (and_6_out, and_2_out, in_9);
  and and_7 (and_7_out, and_3_out, in_9);
  and and_8 (and_8_out, and_4_out, in_9);
  and and_9 (and_9_out, not_1_out, or_1_out);
  and and_10 (and_10_out, or_2_out, not_1_out);
  and and_11 (and_11_out, or_3_out, not_1_out);
  and and_12 (and_12_out, or_4_out, not_1_out);
  or or_5 (out_10, and_5_out, and_9_out);
  or or_6 (out_11, and_6_out, and_10_out);
  or or_7 (out_12, and_7_out, and_11_out);
  or or_8 (out_13, and_8_out, and_12_out);
endmodule

module Exemolo0033 (
  input  [3:0] in_1,
  input  [3:0] in_2,
  input  [3:0] in_3,
  output [3:0] s1,
  output [3:0] s2
);

  wire [3:0] and_1_out, and_2_out, and_3_out, and_4_out, and_5_out, nand_1_out, nor_1_out, not_1_out,
       or_1_out;

  assign and_1_out = in_2 & in_1;  // AND_Gate and_1, 4 bits wide
  assign or_1_out = in_2 | in_1;  // OR_Gate or_1, 4 bits wide
  assign nand_1_out = ~(in_1 & in_2);  // NAND_Gate nand_1, 4 bits wide
  assign nor_1_out = ~(in_1 | in_2);  // NOR_Gate nor_1, 4 bits wide
  assign not_1_out = ~in_3;  // NOT_Gate not_1, 4 bits wide
  assign and_2_out = and_1_out & not_1_out;  // AND_Gate and_2, 4 bits wide
  assign and_3_out = or_1_out & not_1_out;  // AND_Gate and_3, 4 bits wide
  assign and_4_out = nand_1_out & in_3;  // AND_Gate and_4, 4 bits wide
  assign and_5_out = nor_1_out & in_3;  // AND_Gate and_5, 4 bits wide
  assign s1 = and_2_out | and_4_out;  // OR_Gate or_2, 4 bits wide
  assign s2 = and_3_out | and_5_out;  // OR_Gate or_3, 4 bits wide
endmodule

module Exemplo0034 (
  input  [3:0] in_1,
  input  [3:0] in_2,
  input  [3:0] in_3,
  output [3:0] s1,
  output [3:0] s2
);

  wire [3:0] and_1_out, and_2_out, and_3_out, and_4_out, nor_1_out, not_1_out, or_1_out, xnor_1_out,
       xor_1_out;

  assign or_1_out = in_2 | in_1;  // OR_Gate or_1, 4 bits wide
  assign nor_1_out = ~(in_2 | in_1);  // NOR_Gate nor_1, 4 bits wide
  assign xor_1_out = in_1 ^ in_2;  // XOR_Gate xor_1, 4 bits wide
  assign xnor_1_out = ~(in_1 ^ in_2);  // XNOR_Gate xnor_1, 4 bits wide
  assign not_1_out = ~in_3;  // NOT_Gate not_1, 4 bits wide
  assign and_1_out = or_1_out & not_1_out;  // AND_Gate and_1, 4 bits wide
  assign and_2_out = nor_1_out & not_1_out;  // AND_Gate and_2, 4 bits wide
  assign and_3_out = xor_1_out & in_3;  // AND_Gate and_3, 4 bits wide
  assign and_4_out = xnor_1_out & in_3;  // AND_Gate and_4, 4 bits wide
  assign s1 = and_1_out | and_3_out;  // OR_Gate or_2, 4 bits wide
  assign s2 = and_2_out | and_4_out;  // OR_Gate or_3, 4 bits wide
endmodule

module Exemplo0035 (
  input  [3:0] in_1,
  input  [3:0] in_2,
  output [3:0] out_3,
  output [3:0] out_4,
  output [3:0] out_5,
  output [3:0] out_6,
  output [3:0] out_7,
  output [3:0] out_8,
  output [3:0] out_9,
  output [3:0] out_10
);

  assign out_3 = ~in_1;  // NOT_Gate not_1, 4 bits wide
  assign out_4 = ~in_2;  // NOT_Gate not_2, 4 bits wide
  assign out_5 = in_2 | in_1;  // OR_Gate or_1, 4 bits wide
  assign out_6 = in_2 & in_1;  // AND_Gate and_1, 4 bits wide
  assign out_7 = ~(in_2 & in_1);  // NAND_Gate nand_1, 4 bits wide
  assign out_8 = in_2 ^ in_1;  // XOR_Gate xor_1, 4 bits wide
  assign out_9 = ~(in_1 ^ in_2);  // XNOR_Gate xnor_1, 4 bits wide
  assign out_10 = ~(in_2 | in_1);  // NOR_Gate nor_1, 4 bits wide
endmodule
