// Logisim project Exemplo0031_logisim.circ as structural Verilog: 2 circuits, main circuit main
module main (
  input  a0,
  input  a1,
  input  a2,
  input  a3,
  input  b0,
  input  b1,
  input  b2,
  input  b3,
  output s_or0,
  output s_and0,
  output s_or1,
  output s_and1,
  output s_or2,
  output s_and2,
  output s_or3,
  output s_and3
);

  f4 f4_1 (
    .s_or0(s_or0), .s_or1(s_or1), .s_or2(s_or2), .s_or3(s_or3), .a0(a0), .a1(a1), .a2(a2), .a3(a3), .b0(b0),
    .b1(b1), .b2(b2), .b3(b3), .s_and0(s_and0), .s_and1(s_and1), .s_and2(s_and2), .s_and3(s_and3));
endmodule

module f4 (
  input  a0,
  input  a1,
  input  a2,
  input  a3,
  input  b0,
  input  b1,
  input  b2,
  input  b3,
  output s_or0,
  output s_and0,
  output s_or1,
  output s_and1,
  output s_or2,
  output s_and2,
  output s_or3,
  output s_and3
);

  or or_1 (s_or0, a0, b0);
  or or_2 (s_or1, a1, b1);
  or or_3 (s_or2, a2, b2);
  or or_4 (s_or3, a3, b3);
  and and_1 (s_and0, a0, b0);
  and and_2 (s_and1, a1, b1);
  and and_3 (s_and2, a2, b2);
  and and_4 (s_and3, a3, b3);
endmodule
