// Logisim project Exemplo0032_logisim.circ as structural Verilog: 2 circuits, main circuit main
module main (
  input  chave,
  input  a0,
  input  a1,
  input  a2,
  input  a3,
  input  b0,
  input  b1,
  input  b2,
  input  b3,
  output s0,
  output s1,
  output s2,
  output s3
);

  subcircuito subcircuito_1 (
    .chave(chave), .a0(a0), .a1(a1), .a2(a2), .a3(a3), .b0(b0), .b1(b1), .b2(b2), .b3(b3), .s3(s3), .s2(s2),
    .s1(s1), .s0(s0));
endmodule

module subcircuito (
  input  chave,
  input  a0,
  input  a1,
  input  a2,
  input  a3,
  input  b0,
  input  b1,
  input  b2,
  input  b3,
  output s3,
  output s2,
  output s1,
  output s0
);

  wire and_1_out, and_2_out, and_3_out, and_4_out, and_5_out, and_6_out, and_7_out, and_8_out, and_9_out,
       and_10_out, and_11_out, and_12_out, not_1_out, or_1_out, or_2_out, or_3_out, or_4_out;

  and and_1 (and_1_out, or_1_out, chave);
  and and_2 (and_2_out, or_2_out, chave);
  and and_3 (and_3_out, or_3_out, chave);
  and and_4 (and_4_out, or_4_out, chave, chave);
  or or_1 (or_1_out, a0, b0);
  or or_2 (or_2_out, a1, b1);
  or or_3 (or_3_out, a2, b2);
  or or_4 (or_4_out, a3, b3);
  not not_1 (not_1_out, chave);
  or or_5 (s3, and_4_out, and_9_out);
  or or_6 (s2, and_3_out, and_11_out);
  or or_7 (s1, and_2_out, and_10_out);
  or or_8 (s0, and_1_out, and_12_out);
  and and_5 (and_5_out, a0, b0);
  and and_6 (and_6_out, a1, b1);
  and and_7 (and_7_out, a2, b2);
  and and_8 (and_8_out, a3, b3);
  and and_9 (and_9_out, and_8_out, not_1_out);
  and and_10 (and_10_out, and_6_out, not_1_out);
  and and_11 (and_11_out, and_7_out, not_1_out);
  and and_12 (and_12_out, and_5_out, not_1_out);
endmodule
