// Logisim project Exemplo0034_logisim.circ as structural Verilog: 4 circuits, main circuit main
module main (
  input  chave,
  input  a0,
  input  a1,
  input  a2,
  input  a3,
  input  b0,
  input  b1,
  input  b2,
  input  b3,
  output s2_0,
  output s2_1,
  output s2_2,
  output s2_3,
  output s1_0,
  output s1_1,
  output s1_2,
  output s1_3
);

  subcircuito subcircuito_1 (
    .chave(chave), .a0(a0), .a1(a1), .a2(a2), .a3(a3), .b0(b0), .b1(b1), .b2(b2), .b3(b3), .s2_0(s2_0),
    .s2_1(s2_1), .s2_2(s2_2), .s2_3(s2_3), .s1_0(s1_0), .s1_1(s1_1), .s1_2(s1_2), .s1_3(s1_3));  // open: s_or_nor_OR0, s_xor_xnor_XOR0, s_or_nor_OR1, s_xor_xnor_XOR1, s_or_nor_OR2, s_xor_xnor_XOR2, s_or_nor_OR3, s_xor_xnor_XOR3, s_or_nor_NOR0, s_xor_xnor_XNOR0, s_or_nor_NOR1, s_xor_xnor_XNOR1, s_or_nor_NOR2, s_xor_xnor_XNOR2, s_or_nor_NOR3, s_xor_xnor_XNOR3
endmodule

module or_nor (
  input  a0,
  input  a1,
  input  a2,
  input  a3,
  input  b0,
  input  b1,
  input  b2,
  input  b3,
  output s_or0,
  output s_nor0,
  output s_or1,
  output s_nor1,
  output s_or2,
  output s_nor2,
  output s_or3,
  output s_nor3
);

  or or_1 (s_or0, a0, b0);
  or or_2 (s_or1, a1, b1);
  or or_3 (s_or2, a2, b2);
  or or_4 (s_or3, a3, b3);
  nor nor_1 (s_nor0, a0, b0);
  nor nor_2 (s_nor1, a1, b1);
  nor nor_3 (s_nor2, a2, b2);
  nor nor_4 (s_nor3, a3, b3);
endmodule

module xor_xnor (
  input  a0,
  input  a1,
  input  a2,
  input  a3,
  input  b0,
  input  b1,
  input  b2,
  input  b3,
  output s_xor0,
  output s_xnor0,
  output s_xor1,
  output s_xnor1,
  output s_xor2,
  output s_xnor2,
  output s_xor3,
  output s_xnor3
);

  xor xor_1 (s_xor0, a0, b0);
  xor xor_2 (s_xor1, a1, b1);
  xor xor_3 (s_xor2, a2, b2);
  xor xor_4 (s_xor3, a3, b3);
  xnor xnor_1 (s_xnor0, a0, b0);
  xnor xnor_2 (s_xnor1, a1, b1);
  xnor xnor_3 (s_xnor2, a2, b2);
  xnor xnor_4 (s_xnor3, a3, b3);
endmodule

module subcircuito (
  input  chave,
  input  a0,
  input  a1,
  input  a2,
  input  a3,
  input  b0,
  input  b1,
  input  b2,
  input  b3,
  output s2_0,
  output s2_1,
  output s2_2,
  output s2_3,
  output s_or_nor_OR0,
  output s_or_nor_NOR0,
  output s_xor_xnor_XOR0,
  output s_xor_xnor_XNOR0,
  output s_or_nor_OR1,
  output s_or_nor_NOR1,
  output s_xor_xnor_XOR1,
  output s_xor_xnor_XNOR1,
  output s_or_nor_OR2,
  output s_or_nor_NOR2,
  output s_xor_xnor_XOR2,
  output s_xor_xnor_XNOR2,
  output s_or_nor_OR3,
  output s_or_nor_NOR3,
  output s_xor_xnor_XOR3,
  output s_xor_xnor_XNOR3,
  output s1_0,
  output s1_1,
  output s1_2,
  output s1_3
);

  wire and_1_out, and_2_out, and_3_out, and_4_out, and_5_out, and_6_out, and_7_out, and_8_out, and_9_out,
       and_10_out, and_11_out, and_12_out, and_13_out, and_14_out, and_15_out, and_16_out, not_1_out;

  not not_1 (not_1_out, chave);
  or_nor or_nor_1 (
    .s_or0(s_or_nor_OR0), .s_or1(s_or_nor_OR1), .s_or2(s_or_nor_OR2), .s_or3(s_or_nor_OR3), .a0(a0), .a1(a1),
    .a2(a2), .a3(a3), .b0(b0), .b1(b1), .b2(b2), .b3(b3), .s_nor0(s_or_nor_NOR0), .s_nor1(s_or_nor_NOR1),
    .s_nor2(s_or_nor_NOR2), .s_nor3(s_or_nor_NOR3));
  and and_1 (and_1_out, s_or_nor_OR2, not_1_out);
  and and_2 (and_2_out, s_or_nor_OR3, not_1_out);
  and and_3 (and_3_out, s_or_nor_OR1, not_1_out);
  and and_4 (and_4_out, s_or_nor_OR0, not_1_out);
  or or_1 (s1_0, and_4_out, and_5_out);
  or or_2 (s1_1, and_3_out, and_6_out);
  or or_3 (s1_2, and_1_out, and_7_out);
  or or_4 (s1_3, and_2_out, and_8_out);
  and and_5 (and_5_out, chave, s_xor_xnor_XOR0);
  and and_6 (and_6_out, chave, s_xor_xnor_XOR1);
  and and_7 (and_7_out, chave, s_xor_xnor_XOR2);
  and and_8 (and_8_out, chave, s_xor_xnor_XOR3);
  xor_xnor xor_xnor_1 (
    .s_xor0(s_xor_xnor_XOR0), .s_xor1(s_xor_xnor_XOR1), .s_xor2(s_xor_xnor_XOR2), .s_xor3(s_xor_xnor_XOR3),
    .a0(a0), .a1(a1), .a2(a2), .a3(a3), .b0(b0), .b1(b1), .b2(b2), .b3(b3), .s_xnor0(s_xor_xnor_XNOR0),
    .s_xnor1(s_xor_xnor_XNOR1), .s_xnor2(s_xor_xnor_XNOR2), .s_xnor3(s_xor_xnor_XNOR3));
  and and_9 (and_9_out, not_1_out, s_or_nor_NOR0);
  or or_5 (s2_0, and_9_out, and_10_out);
  and and_10 (and_10_out, chave, s_xor_xnor_XNOR0);
  and and_11 (and_11_out, not_1_out, s_or_nor_NOR1);
  or or_6 (s2_1, and_11_out, and_12_out);
  and and_12 (and_12_out, chave, s_xor_xnor_XNOR1);
  and and_13 (and_13_out, not_1_out, s_or_nor_NOR2);
  or or_7 (s2_2, and_13_out, and_14_out);
  and and_14 (and_14_out, chave, s_xor_xnor_XNOR2);
  and and_15 (and_15_out, not_1_out, s_or_nor_NOR3);
  or or_8 (s2_3, and_15_out, and_16_out);
  and and_16 (and_16_out, chave, s_xor_xnor_XNOR3);
endmodule
