// Logisim project circuitos.circ as structural Verilog
module Ex01 (
  input  [3:0] in_1,
  input  [3:0] in_2,
  output [3:0] Saida_AND,
  output [3:0] Saida_OR
);

  assign Saida_AND = in_1 & in_2;  // AND_Gate and_1, 4 bits wide
  assign Saida_OR = in_1 | in_2;  // OR_Gate or_1, 4 bits wide
endmodule

module Ex02 (
  input  [3:0] in_1,
  input  [3:0] in_2,
  input  [3:0] _0_OR___1_AND,
  output [3:0] out_4
);

  wire [3:0] and_1_out, and_2_out, ex01_1_saida_and, ex01_1_saida_or;

  Ex01 ex01_1 (.in_1(in_1), .in_2(in_2), .Saida_AND(ex01_1_saida_and), .Saida_OR(ex01_1_saida_or));
  assign and_1_out = ex01_1_saida_and & _0_OR___1_AND;  // AND_Gate and_1, 4 bits wide
  assign and_2_out = ex01_1_saida_or & ~_0_OR___1_AND;  // AND_Gate and_2, 4 bits wide
  assign out_4 = and_1_out | and_2_out;  // OR_Gate or_1, 4 bits wide
endmodule

module Ex03 (
  input  [3:0] _0_OR_AND_1_NOR_NAND,
  input  [3:0] in_2,
  input  [3:0] in_3,
  output [3:0] NOR_ou_AND,
  output [3:0] OR_ou_NAND
);

  wire [3:0] and_1_out, and_2_out, and_3_out, and_4_out, AND_OR_saida_and, AND_OR_saida_or, nand_1_out,
       nor_1_out;

  Ex01 AND_OR (.in_1(in_2), .in_2(in_3), .Saida_AND(AND_OR_saida_and), .Saida_OR(AND_OR_saida_or));
  assign nor_1_out = ~(in_2 | in_3);  // NOR_Gate nor_1, 4 bits wide
  assign nand_1_out = ~(in_2 & in_3);  // NAND_Gate nand_1, 4 bits wide
  assign and_1_out = ~_0_OR_AND_1_NOR_NAND & AND_OR_saida_and;  // AND_Gate and_1, 4 bits wide
  assign and_2_out = nor_1_out & _0_OR_AND_1_NOR_NAND;  // AND_Gate and_2, 4 bits wide
  assign and_3_out = AND_OR_saida_or & ~_0_OR_AND_1_NOR_NAND;  // AND_Gate and_3, 4 bits wide
  assign NOR_ou_AND = and_1_out | and_2_out;  // OR_Gate or_1, 4 bits wide
  assign OR_ou_NAND = and_3_out | and_4_out;  // OR_Gate or_2, 4 bits wide
  assign and_4_out = _0_OR_AND_1_NOR_NAND & nand_1_out;  // AND_Gate and_4, 4 bits wide

  // Notes on the sheet:
  //   z
  //   s1
  //   s5
  //   s4
  //   s6
  //   s7
endmodule

module Ex04 (
  input  [3:0] in_1,
  input  [3:0] in_2,
  input  [3:0] in_3,
  output [3:0] _0_OR_1_XNOR,
  output [3:0] _0_NOR_1_XOR
);

  wire [3:0] and_1_out, and_2_out, or_1_out, xor_1_out;

  assign xor_1_out = in_1 ^ in_2;  // XOR_Gate xor_1, 4 bits wide
  assign or_1_out = in_1 | in_2;  // OR_Gate or_1, 4 bits wide
  assign and_1_out = xor_1_out & ~in_3;  // AND_Gate and_1, 4 bits wide
  assign and_2_out = or_1_out & in_3;  // AND_Gate and_2, 4 bits wide
  assign _0_OR_1_XNOR = and_2_out | and_1_out;  // OR_Gate or_2, 4 bits wide
  assign _0_NOR_1_XOR = ~_0_OR_1_XNOR;  // NOT_Gate not_1, 4 bits wide
endmodule

module Ex05 (
  input  [3:0] in_1,
  input  [3:0] in_2,
  output [3:0] out_3,
  output [3:0] out_4,
  output [3:0] out_5,
  output [3:0] out_6,
  output [3:0] out_7,
  output [3:0] out_8,
  output [3:0] out_9,
  output [3:0] out_10
);

  assign out_3 = ~in_2;  // NOT_Gate not_1, 4 bits wide
  assign out_4 = ~in_1;  // NOT_Gate not_2, 4 bits wide
  assign out_6 = in_2 | in_1;  // OR_Gate or_1, 4 bits wide
  assign out_8 = in_2 & in_1;  // AND_Gate and_1, 4 bits wide
  assign out_10 = in_2 ^ in_1;  // XOR_Gate xor_1, 4 bits wide
  assign out_5 = ~out_6;  // NOT_Gate not_3, 4 bits wide
  assign out_7 = ~out_8;  // NOT_Gate not_4, 4 bits wide
  assign out_9 = ~out_10;  // NOT_Gate not_5, 4 bits wide
endmodule
