// Logisim project Exemplo0031.circ as structural Verilog
module Exemplo0031 (
  input  [3:0] A,
  input  [3:0] B,
  output out_3,
  output out_4,
  output out_5,
  output out_6,
  output out_7,
  output out_8,
  output out_9,
  output out_10
);

  assign {out_3, out_4, out_5, out_6} = A | B;  // OR_Gate or_1, 4 bits wide
  assign {out_7, out_8, out_9, out_10} = A & B;  // AND_Gate and_1, 4 bits wide
endmodule
