// Logisim project Exemplo0032.circ as structural Verilog: 1 circuit, main circuit main
module main (
  input  [3:0] Selecionador,
  input  [3:0] X,
  input  [3:0] Y,
  output [3:0] \Saída 
);

  wire [3:0] AND_1_out, AND_2_out, AND_3_out, NOT_out, OR_1_out;

  assign AND_1_out = X & Y;  // AND_Gate AND_1, 4 bits wide
  assign AND_2_out = Selecionador & AND_1_out;  // AND_Gate AND_2, 4 bits wide
  assign NOT_out = ~Selecionador;  // NOT_Gate NOT, 4 bits wide
  assign \Saída  = AND_2_out | AND_3_out;  // OR_Gate OR_2, 4 bits wide
  assign OR_1_out = Y | X;  // OR_Gate OR_1, 4 bits wide
  assign AND_3_out = NOT_out & OR_1_out;  // AND_Gate AND_3, 4 bits wide

  // Notes on the sheet:
  //   Selecionador
  //   1 = AND  /  0 = OR
endmodule
