// Logisim project Exemplo0033.circ as structural Verilog: 1 circuit, main circuit main
module main (
  input  [3:0] X,
  input  [3:0] Y,
  input  [3:0] Selecionador,
  output [3:0] \Saída ,
  output [3:0] \Saída_2 ,
  output [3:0] \Saída_3 ,
  output [3:0] \Saída_4 
);

  wire [3:0] AND_1_out, NAND1_out, NOR1_out, NOT_out, OR_1_out;

  assign AND_1_out = X & Y;  // AND_Gate AND_1, 4 bits wide
  assign \Saída  = Selecionador & AND_1_out;  // AND_Gate AND_2, 4 bits wide
  assign \Saída_2  = Selecionador & OR_1_out;  // AND_Gate AND_3, 4 bits wide
  assign OR_1_out = Y | X;  // OR_Gate OR_1, 4 bits wide
  assign NOT_out = ~Selecionador;  // NOT_Gate NOT, 4 bits wide
  assign NAND1_out = ~(Y & X);  // NAND_Gate NAND1, 4 bits wide
  assign \Saída_3  = NOT_out & NAND1_out;  // AND_Gate AND_4, 4 bits wide
  assign NOR1_out = ~(X | Y);  // NOR_Gate NOR1, 4 bits wide
  assign \Saída_4  = NOT_out & NOR1_out;  // AND_Gate AND_5, 4 bits wide

  // Notes on the sheet:
  //   Selecionador
  //   0 = NAND e NOR
  //   1 = AND e OR
endmodule
