// Logisim project Exemplo0034.circ as structural Verilog: 1 circuit, main circuit main
module main (
  input  [3:0] X,
  input  [3:0] Y,
  input  [3:0] Selecionador,
  output [3:0] \Saída ,
  output [3:0] \Saída_2 ,
  output [3:0] \Saída_3 ,
  output [3:0] \Saída_4 
);

  wire [3:0] NOR1_out, NOT_out, OR_1_out, XNOR_1_out, XOR_1_out;

  assign OR_1_out = X | Y;  // OR_Gate OR_1, 4 bits wide
  assign \Saída  = Selecionador & OR_1_out;  // AND_Gate AND_2, 4 bits wide
  assign \Saída_2  = Selecionador & NOR1_out;  // AND_Gate AND_3, 4 bits wide
  assign NOR1_out = ~(Y | X);  // NOR_Gate NOR1, 4 bits wide
  assign NOT_out = ~Selecionador;  // NOT_Gate NOT, 4 bits wide
  assign XOR_1_out = Y ^ X;  // XOR_Gate XOR_1, 4 bits wide
  assign \Saída_3  = NOT_out & XOR_1_out;  // AND_Gate AND_4, 4 bits wide
  assign XNOR_1_out = ~(X ^ Y);  // XNOR_Gate XNOR_1, 4 bits wide
  assign \Saída_4  = NOT_out & XNOR_1_out;  // AND_Gate AND_5, 4 bits wide

  // Notes on the sheet:
  //   Selecionador
  //   0 = XOR e XNOR
  //   1 = OR e NOR
endmodule
