// Logisim project Exemplo0035.circ as structural Verilog: 1 circuit, main circuit main
module main (
  input  [3:0] X,
  input  [3:0] Y,
  output [3:0] s2,
  output [3:0] s1,
  output [3:0] s3,
  output [3:0] s5,
  output [3:0] s7,
  output [3:0] s4,
  output [3:0] s6,
  output [3:0] s8
);

  assign s1 = ~X;  // NOT_Gate NOT, 4 bits wide
  assign s2 = X | Y;  // OR_Gate OR, 4 bits wide
  assign s4 = ~(X & Y);  // NAND_Gate NAND, 4 bits wide
  assign s3 = ~(X | Y);  // NOR_Gate NOR, 4 bits wide
  assign s5 = X & Y;  // AND_Gate AND, 4 bits wide
  assign s6 = ~(X ^ Y);  // XNOR_Gate XNOR, 4 bits wide
  assign s8 = ~Y;  // NOT_Gate NOT_2, 4 bits wide
  assign s7 = X ^ Y;  // XOR_Gate XOR, 4 bits wide
endmodule
