// Logisim project Exemplos01-03.circ as structural Verilog: 3 circuits, main circuit main
module main (
  input  [3:0] pinoA,
  input  [3:0] pinoB,
  input  [3:0] pinoA_2,
  input  [3:0] pinoB_2,
  input  [3:0] pinoA_3,
  input  [3:0] pinoB_3,
  input  [3:0] ch,
  output [3:0] s1,
  output [3:0] s2,
  output [3:0] s1_2,
  output [3:0] s1_3,
  output [3:0] s1_4
);

  wire [3:0] and_1_out, and_2_out, and_3_out, and_4_out, and_5_out, and_7_out, and_or_1_s1, and_or_1_s2,
       nand_1_out, nand_nor_1__1, or_2_out, undriven;

  And_Or and_or_1 (.pinoA(pinoB_3), .pinoB(pinoA_3), .s1(and_or_1_s1), .s2(and_or_1_s2));
  Nand_Nor nand_nor_1 (._1(nand_nor_1__1), .s2(ch));  // open: s1, _1_2
  assign s2 = pinoA | pinoB;  // OR_Gate or_1, 4 bits wide
  assign and_1_out = pinoB_2 & pinoA_2;  // AND_Gate and_1, 4 bits wide
  assign or_2_out = pinoA_2 | pinoB_2;  // OR_Gate or_2, 4 bits wide
  assign and_2_out = and_or_1_s1 & ch;  // AND_Gate and_2, 4 bits wide
  assign and_3_out = and_or_1_s2 & ch;  // AND_Gate and_3, 4 bits wide
  assign ch = ~ch;  // NOT_Gate not_1, 4 bits wide
  assign and_4_out = ch & nand_nor_1__1;  // AND_Gate and_4, 4 bits wide
  assign and_5_out = ch & ch;  // AND_Gate and_5, 4 bits wide
  assign s1 = pinoB & pinoA;  // AND_Gate and_6, 4 bits wide
  assign and_7_out = and_1_out & undriven;  // AND_Gate and_7, 4 bits wide
  assign nand_1_out = ~(or_2_out & undriven);  // NAND_Gate nand_1, 4 bits wide
  assign s1_2 = and_7_out | nand_1_out;  // OR_Gate or_3, 4 bits wide
  assign s1_3 = and_2_out | and_4_out;  // OR_Gate or_4, 4 bits wide
  assign s1_4 = and_3_out | and_5_out;  // OR_Gate or_5, 4 bits wide

  // Notes on the sheet:
  //   exemplo 01
  //        exemplo 02
  //    exemplo 03
endmodule

module And_Or (
  input  [3:0] pinoA,
  input  [3:0] pinoB,
  output [3:0] s1,
  output [3:0] s2
);

  assign s1 = pinoA & pinoB;  // AND_Gate and_1, 4 bits wide
  assign s2 = pinoA | pinoB;  // OR_Gate or_1, 4 bits wide
endmodule

module Nand_Nor (
  input  [3:0] s1,
  input  [3:0] s2,
  output [3:0] _1,
  output [3:0] _1_2
);

  assign _1 = ~(s1 & s2);  // NAND_Gate nand_1, 4 bits wide
  assign _1_2 = ~(s1 | s2);  // NOR_Gate nor_1, 4 bits wide
endmodule
