// Logisim project Exemplos04-05.circ as structural Verilog: 5 circuits, main circuit main
module main (
  input  [3:0] pinoa,
  input  [3:0] pinob,
  input  [3:0] pinoa_2,
  input  [3:0] pinob_2,
  output [3:0] out_5,
  output [3:0] out_6,
  output [3:0] out_7,
  output [3:0] out_8,
  output [3:0] out_9,
  output [3:0] out_10,
  output [3:0] out_11,
  output [3:0] out_12
);

  wire [3:0] and_1_out, and_2_out, and_3_out, and_4_out, not_1_out, undriven;

  assign not_1_out = ~undriven;  // NOT_Gate not_1, 4 bits wide
  and_or and_or_1 (.pinoa(pinoa_2), .pinob(pinob_2), .\and (out_9));  // open: or
  Xnor_Xor xnor_xor_1 (.pinoa(pinob_2), .pinob(pinoa_2), .Xor(out_10), .Xnor(out_11));
  Nor_Nand nor_nand_1 (.pinoa(pinoa_2), .pinob(pinob_2), .out_4(out_11));  // open: out_3
  assign and_1_out = pinoa & not_1_out;  // AND_Gate and_1, 4 bits wide
  assign and_2_out = not_1_out & pinob;  // AND_Gate and_2, 4 bits wide
  assign and_3_out = pinoa & undriven;  // AND_Gate and_3, 4 bits wide
  assign and_4_out = pinob & undriven;  // AND_Gate and_4, 4 bits wide
  Xnor_Xor xnor_xor_2 (.pinoa(and_3_out), .pinob(and_4_out), .Xor(out_7), .Xnor(out_8));
  Or_Nor or_nor_1 (.pinoa(and_1_out), .pinob(and_2_out), .out_3(out_5), .out_4(out_6));

  assign out_12 = out_11;

  // Notes on the sheet:
  //                    exemplo04
  //                 exemplo05
endmodule

module and_or (
  input  [3:0] pinoa,
  input  [3:0] pinob,
  output [3:0] \and ,
  output [3:0] \or 
);

  assign \and  = pinoa & pinob;  // AND_Gate and_1, 4 bits wide
  assign \or  = pinob | pinoa;  // OR_Gate or_1, 4 bits wide
endmodule

module Nor_Nand (
  input  [3:0] pinoa,
  input  [3:0] pinob,
  output [3:0] out_3,
  output [3:0] out_4
);

  assign out_3 = ~(pinoa & pinob);  // NAND_Gate nand_1, 4 bits wide
  assign out_4 = ~(pinoa | pinob);  // NOR_Gate nor_1, 4 bits wide
endmodule

module Xnor_Xor (
  input  [3:0] pinoa,
  input  [3:0] pinob,
  output [3:0] Xor,
  output [3:0] Xnor
);

  assign Xor = pinoa ^ pinob;  // XOR_Gate xor_1, 4 bits wide
  assign Xnor = ~pinoa;  // XNOR_Gate xnor_1, 4 bits wide XNOR_Gate
endmodule

module Or_Nor (
  input  [3:0] pinoa,
  input  [3:0] pinob,
  output [3:0] out_3,
  output [3:0] out_4
);

  assign out_3 = pinoa | pinob;  // OR_Gate or_1, 4 bits wide
  assign out_4 = ~(pinob | pinoa);  // NOR_Gate nor_1, 4 bits wide
endmodule
