// Logisim project Exemplo0031.circ as structural Verilog: 1 circuit, main circuit main
module main (
  input  [3:0] x,
  input  [3:0] y,
  output [3:0] z,
  output [3:0] w
);

  assign z = x & y;  // AND_Gate and, 4 bits wide
  assign w = x | y;  // OR_Gate or, 4 bits wide

  // Notes on the sheet:
  //   Mateus Augusto Moraes Ferreira     Matricula: 435669
endmodule
