// Logisim project Exemplo0032.circ as structural Verilog: 1 circuit, main circuit main
module main (
  input  [3:0] x,
  input  [3:0] y,
  input  [3:0] chave,
  output [3:0] s
);

  wire [3:0] and_1_out, and_2_out, and_3_out, not_1_out, or_1_out;

  assign and_1_out = x & y;  // AND_Gate and_1, 4 bits wide
  assign not_1_out = ~chave;  // NOT_Gate not_1, 4 bits wide
  assign or_1_out = x | y;  // OR_Gate or_1, 4 bits wide
  assign and_2_out = and_1_out & not_1_out;  // AND_Gate and_2, 4 bits wide
  assign and_3_out = or_1_out & chave;  // AND_Gate and_3, 4 bits wide
  assign s = and_2_out | and_3_out;  // OR_Gate or_2, 4 bits wide

  // Notes on the sheet:
  //   Chave  0-OR / 1-AND
  //   Mateus Augusto Moraes Ferreira     Matrícula:435669
endmodule
