// Logisim project Exemplo0033.circ as structural Verilog: 1 circuit, main circuit main
module main (
  input  [3:0] x,
  input  [3:0] y,
  input  [3:0] chave,
  output [3:0] s1,
  output [3:0] s2,
  output [3:0] s3,
  output [3:0] s4
);

  wire [3:0] and1_out, nand1_out, not_1_out, or1_out, or2_out;

  assign nand1_out = ~(x & y);  // NAND_Gate nand1, 4 bits wide
  assign or1_out = ~(x | y);  // NOR_Gate or1, 4 bits wide
  assign not_1_out = ~chave;  // NOT_Gate not_1, 4 bits wide
  assign and1_out = x & y;  // AND_Gate and1, 4 bits wide
  assign or2_out = x | y;  // OR_Gate or2, 4 bits wide
  assign s1 = nand1_out & not_1_out;  // AND_Gate and2, 4 bits wide
  assign s2 = or1_out & not_1_out;  // AND_Gate and3, 4 bits wide
  assign s3 = chave & and1_out;  // AND_Gate and4, 4 bits wide
  assign s4 = chave & or2_out;  // AND_Gate and5, 4 bits wide

  // Notes on the sheet:
  //   w1
  //   w2
  //   nchave
  //   w3
  //   w4
  //   Mateus Augusto Moraes Ferreira   Matricula: 435669
endmodule
