// Logisim project Exemplo0034.circ as structural Verilog: 1 circuit, main circuit main
module main (
  input  [3:0] x,
  input  [3:0] y,
  input  [3:0] chave,
  output [3:0] s1,
  output [3:0] s2,
  output [3:0] s3,
  output [3:0] s4
);

  wire [3:0] nor_1_out, not_1_out, or_1_out, xnor_1_out, xor_1_out;

  assign or_1_out = x | y;  // OR_Gate or_1, 4 bits wide
  assign nor_1_out = ~(x | y);  // NOR_Gate nor_1, 4 bits wide
  assign not_1_out = ~chave;  // NOT_Gate not_1, 4 bits wide
  assign xor_1_out = x ^ y;  // XOR_Gate xor_1, 4 bits wide
  assign xnor_1_out = ~(x ^ y);  // XNOR_Gate xnor_1, 4 bits wide
  assign s1 = or_1_out & not_1_out;  // AND_Gate and2, 4 bits wide
  assign s2 = nor_1_out & not_1_out;  // AND_Gate and3, 4 bits wide
  assign s3 = chave & xor_1_out;  // AND_Gate and4, 4 bits wide
  assign s4 = chave & xnor_1_out;  // AND_Gate and5, 4 bits wide

  // Notes on the sheet:
  //   w1
  //   w2
  //   nchave
  //   w3
  //   w4
  //   Mateus Augusto Moraes Ferreira   Matricula: 435669
endmodule
