// Logisim project Exemplo0035.circ as structural Verilog: 1 circuit, main circuit main
module main (
  input  [3:0] x,
  input  [3:0] y,
  output [3:0] s0,
  output [3:0] s1,
  output [3:0] s2,
  output [3:0] s3,
  output [3:0] s4,
  output [3:0] s5,
  output [3:0] s6,
  output [3:0] s7
);

  assign s0 = ~x;  // NOT_Gate not_1, 4 bits wide
  assign s1 = ~y;  // NOT_Gate not_2, 4 bits wide
  assign s2 = x & y;  // AND_Gate and1, 4 bits wide
  assign s3 = ~(x & y);  // NAND_Gate nand1, 4 bits wide
  assign s4 = x | y;  // OR_Gate or1, 4 bits wide
  assign s5 = ~(x | y);  // NOR_Gate nor1, 4 bits wide
  assign s6 = x ^ y;  // XOR_Gate xor1, 4 bits wide
  assign s7 = ~(x ^ y);  // XNOR_Gate xnor1, 4 bits wide

  // Notes on the sheet:
  //   Mateus Augusto Moraes Ferreira    Matricula: 435669
endmodule
