// Logisim project Exemplo0022.circ as structural Verilog: 1 circuit, main circuit main
module main (
  input  [3:0] in_1,
  input  [3:0] in_2,
  input  [3:0] _0_OR_1_AND,
  output [3:0] out_4
);

  wire [3:0] and_1_out, and_2_out, and_3_out, not_1_out, or_1_out;

  assign or_1_out = in_1 | in_2;  // OR_Gate or_1, 4 bits wide
  assign not_1_out = ~_0_OR_1_AND;  // NOT_Gate not_1, 4 bits wide
  assign and_1_out = in_1 & in_2;  // AND_Gate and_1, 4 bits wide
  assign and_2_out = or_1_out & not_1_out;  // AND_Gate and_2, 4 bits wide
  assign and_3_out = and_1_out & _0_OR_1_AND;  // AND_Gate and_3, 4 bits wide
  assign out_4 = and_2_out ^ and_3_out;  // XOR_Gate xor_1, 4 bits wide
endmodule
