// Logisim project Exemplo0023.circ as structural Verilog: 1 circuit, main circuit main
module main (
  input  [3:0] in_1,
  input  [3:0] in_2,
  input  [3:0] _0_OR_AND_1_NOR_NAND,
  output [3:0] _0_OR_1_NOR,
  output [3:0] _0_AND_1_NAND
);

  wire [3:0] and_1_out, and_2_out, and_3_out, and_4_out, and_5_out, nand_1_out, nor_1_out, not_1_out,
       or_1_out;

  assign or_1_out = in_1 | in_2;  // OR_Gate or_1, 4 bits wide
  assign and_1_out = in_1 & in_2;  // AND_Gate and_1, 4 bits wide
  assign not_1_out = ~_0_OR_AND_1_NOR_NAND;  // NOT_Gate not_1, 4 bits wide
  assign nor_1_out = ~(in_1 | in_2);  // NOR_Gate nor_1, 4 bits wide
  assign nand_1_out = ~(in_1 & in_2);  // NAND_Gate nand_1, 4 bits wide
  assign and_2_out = or_1_out & not_1_out;  // AND_Gate and_2, 4 bits wide
  assign and_3_out = and_1_out & not_1_out;  // AND_Gate and_3, 4 bits wide
  assign and_4_out = nor_1_out & _0_OR_AND_1_NOR_NAND;  // AND_Gate and_4, 4 bits wide
  assign and_5_out = nand_1_out & _0_OR_AND_1_NOR_NAND;  // AND_Gate and_5, 4 bits wide
  assign _0_OR_1_NOR = and_2_out ^ and_4_out;  // XOR_Gate xor_1, 4 bits wide
  assign _0_AND_1_NAND = and_3_out ^ and_5_out;  // XOR_Gate xor_2, 4 bits wide
endmodule
