// Logisim project Exemplo0024.circ as structural Verilog: 1 circuit, main circuit main
module main (
  input  [3:0] in_1,
  input  [3:0] in_2,
  input  [3:0] _0_OR_NOR_1_XOR_XNOR,
  output [3:0] _0_OR_1_XOR,
  output [3:0] _0_NOR_1_XNOR
);

  wire [3:0] and_1_out, and_2_out, and_3_out, and_4_out, nor_1_out, not_1_out, or_1_out, xnor_1_out,
       xor_1_out;

  assign or_1_out = in_1 | in_2;  // OR_Gate or_1, 4 bits wide
  assign nor_1_out = ~(in_1 | in_2);  // NOR_Gate nor_1, 4 bits wide
  assign not_1_out = ~_0_OR_NOR_1_XOR_XNOR;  // NOT_Gate not_1, 4 bits wide
  assign xor_1_out = in_1 ^ in_2;  // XOR_Gate xor_1, 4 bits wide
  assign xnor_1_out = ~(in_1 ^ in_2);  // XNOR_Gate xnor_1, 4 bits wide
  assign and_1_out = or_1_out & not_1_out;  // AND_Gate and_1, 4 bits wide
  assign and_2_out = nor_1_out & not_1_out;  // AND_Gate and_2, 4 bits wide
  assign and_3_out = xor_1_out & _0_OR_NOR_1_XOR_XNOR;  // AND_Gate and_3, 4 bits wide
  assign and_4_out = xnor_1_out & _0_OR_NOR_1_XOR_XNOR;  // AND_Gate and_4, 4 bits wide
  assign _0_OR_1_XOR = and_1_out ^ and_3_out;  // XOR_Gate xor_2, 4 bits wide
  assign _0_NOR_1_XNOR = and_2_out ^ and_4_out;  // XOR_Gate xor_3, 4 bits wide
endmodule
