// Logisim project Exemplo0025.circ as structural Verilog: 1 circuit, main circuit main
module main (
  input  [3:0] in_1,
  input  [3:0] in_2,
  output [3:0] out_3,
  output [3:0] out_4,
  output [3:0] out_5,
  output [3:0] out_6,
  output [3:0] out_7,
  output [3:0] out_8,
  output [3:0] out_9,
  output [3:0] out_10
);

  assign out_3 = ~in_1;  // NOT_Gate not_1, 4 bits wide
  assign out_4 = in_1 & in_2;  // AND_Gate and_1, 4 bits wide
  assign out_5 = in_1 | in_2;  // OR_Gate or_1, 4 bits wide
  assign out_6 = ~(in_1 & in_2);  // NAND_Gate nand_1, 4 bits wide
  assign out_7 = ~(in_1 | in_2);  // NOR_Gate nor_1, 4 bits wide
  assign out_8 = in_1 ^ in_2;  // XOR_Gate xor_1, 4 bits wide
  assign out_9 = ~(in_1 ^ in_2);  // XNOR_Gate xnor_1, 4 bits wide
  assign out_10 = ~in_2;  // NOT_Gate not_2, 4 bits wide
endmodule
