// Logisim project Exemplo0031.circ as structural Verilog: 1 circuit, main circuit main
module main (
  input  [3:0] x,
  input  [3:0] y,
  output [3:0] z1,
  output [3:0] z0
);

  assign z1 = x | y;  // OR_Gate or_1, 4 bits wide
  assign z0 = y & x;  // AND_Gate and_1, 4 bits wide

  // Notes on the sheet:
  //   438964 - Ederson Cristiano Nunes
endmodule
