// Logisim project Exemplo0032.circ as structural Verilog: 1 circuit, main circuit main
module main (
  input  [3:0] x,
  input  [3:0] y,
  input  [3:0] chave,
  output [3:0] z0
);

  wire [3:0] and_1_out, and_2_out, not_1_out;

  assign not_1_out = ~chave;  // NOT_Gate not_1, 4 bits wide
  assign and_1_out = x & not_1_out;  // AND_Gate and_1, 4 bits wide
  assign and_2_out = y & chave;  // AND_Gate and_2, 4 bits wide
  assign z0 = and_1_out | and_2_out;  // OR_Gate or_1, 4 bits wide

  // Notes on the sheet:
  //   438964 - Ederson Cristiano Nunes
endmodule
