// Logisim project Exemplo0032.circ as structural Verilog: 1 circuit, main circuit main
module main (
  input  [3:0] in_1,
  input  [3:0] in_2,
  input  in_3,
  input  [3:0] in_4
);

  wire and_1_out, or_1_out, or_2_out, undriven;

  and and_1 (and_1_out, in_1[0], undriven);
  or or_1 (or_1_out, in_3, in_3);
  or or_2 (or_2_out, and_1_out, or_1_out);
  // Pins of 1 and 4 bits meet at {in_4[3:1], in_3}
  // Pins of 1 and 4 bits meet at in_1

  assign in_4[0] = in_3;
endmodule
