// Logisim project Exemplo0033.circ as structural Verilog: 1 circuit, main circuit main
module main (
  input  [3:0] in_1,
  input  [3:0] in_2,
  input  in_3,
  output [3:0] out_4
);

  wire and_1_out, and_2_out, or_1_out, or_2_out, or_3_out;

  and and_1 (and_1_out, in_1[0], in_2[0]);
  or or_1 (or_1_out, in_1[0], in_2[0]);
  not not_1 (in_3, and_1_out);
  not not_2 (in_3, or_1_out);
  buf and_2 (and_2_out, in_3);  // AND_Gate
  buf or_2 (or_2_out, in_3);  // OR_Gate
  or or_3 (or_3_out, and_2_out, or_2_out);
  // Pins of 1 and 4 bits meet at in_2
  // Pins of 1 and 4 bits meet at in_1
endmodule
