// Logisim project Exemplo0034.circ as structural Verilog: 1 circuit, main circuit main
module main (
  input  [3:0] in_1,
  input  [3:0] in_2,
  input  in_3,
  output [3:0] out_4
);

  wire nor_1_out, or_1_out, or_2_out;

  xor xor_1 (in_3, in_1[0], in_2[0]);
  xnor xnor_1 (in_3, in_1[0], in_2[0]);
  buf or_1 (or_1_out, in_3);  // OR_Gate
  not nor_1 (nor_1_out, in_3);  // NOR_Gate
  or or_2 (or_2_out, or_1_out, nor_1_out);
  // Pins of 1 and 4 bits meet at in_1
  // Pins of 1 and 4 bits meet at in_2
endmodule
