// Logisim project Exemplo0035.circ as structural Verilog: 1 circuit, main circuit main
module main (
  input  in_1,
  input  in_2,
  output out_3,
  output out_4,
  output out_5,
  output out_6,
  output out_7,
  output out_8,
  output out_9,
  output out_10
);

  wire and_1_out, nand_1_out, nor_1_out, not_1_out, not_2_out, or_1_out, xnor_1_out, xor_1_out;

  and and_1 (and_1_out, in_2, in_1);
  or or_1 (or_1_out, in_2, in_1);
  not not_1 (not_1_out, in_1);
  not not_2 (not_2_out, in_1);
  nand nand_1 (nand_1_out, in_1, in_2, in_2);
  nor nor_1 (nor_1_out, in_1, in_2);
  buf xor_1 (xor_1_out, in_2);  // XOR_Gate
  xnor xnor_1 (xnor_1_out, in_2, in_1);
endmodule
