// Logisim project Exemplo0031.circ as structural Verilog: 1 circuit, main circuit main
module main (
  input  [3:0] a,
  input  [3:0] b,
  output [3:0] s2,
  output [3:0] s1
);

  assign s2 = a | b;  // OR_Gate o0, 4 bits wide
  assign s1 = a & b;  // AND_Gate a0, 4 bits wide

  // Notes on the sheet:
  //   438964 - Ederson Cristiano Nunes
endmodule
