// Logisim project Exemplo0033.circ as structural Verilog: 1 circuit, main circuit main
module main (
  input  [3:0] x,
  input  [3:0] y,
  input  [3:0] z,
  output [3:0] s5
);

  wire [3:0] and1_out, and2_out, and3_out, not_1_out, or1_out;

  assign and1_out = x & y;  // AND_Gate and1, 4 bits wide
  assign not_1_out = ~z;  // NOT_Gate not_1, 4 bits wide
  assign and2_out = and1_out & not_1_out;  // AND_Gate and2, 4 bits wide
  assign or1_out = x | y;  // OR_Gate or1, 4 bits wide
  assign and3_out = not_1_out & or1_out;  // AND_Gate and3, 4 bits wide
  assign s5 = and2_out | and3_out;  // OR_Gate or2, 4 bits wide

  // Notes on the sheet:
  //   Ederson Cristiano Nunes - 438964
  //   s1
  //   s3
  //   s2
  //   s4
endmodule
