// Logisim project Exemplo0032.circ as structural Verilog: 1 circuit, main circuit main
module main (
  input  [3:0] in_1,
  input  [3:0] in_2,
  input  [3:0] in_3,
  output [3:0] out_4
);

  wire [3:0] and_1_out, and_2_out, not_1_out, or_1_out, or_2_out;

  assign and_1_out = in_1 & in_2;  // AND_Gate and_1, 4 bits wide
  assign not_1_out = ~in_3;  // NOT_Gate not_1, 4 bits wide
  assign or_1_out = in_1 | in_2;  // OR_Gate or_1, 4 bits wide
  assign and_2_out = and_1_out & not_1_out;  // AND_Gate and_2, 4 bits wide
  assign or_2_out = or_1_out | in_3;  // OR_Gate or_2, 4 bits wide
  assign out_4 = and_2_out | or_2_out;  // OR_Gate or_3, 4 bits wide

  // Notes on the sheet:
  //   0 = or | 1 = and
  //   luiz marques de olieira - 417138
endmodule
