// Logisim project Extra01.circ as structural Verilog: 1 circuit, main circuit main
module main (
  input  [3:0] X,
  input  [3:0] Y,
  input  [3:0] in_3,
  output [3:0] out_4
);

  wire [3:0] and_1_out, and_2_out, not_1_out, not_2_out, or_1_out, xor_1_out, xor_2_out, xor_3_out, xor_4_out;

  assign xor_1_out = X ^ Y;  // XOR_Gate xor_1, 4 bits wide
  assign xor_2_out = X ^ Y;  // XOR_Gate xor_2, 4 bits wide
  assign not_1_out = ~or_1_out;  // NOT_Gate not_1, 4 bits wide
  assign and_1_out = in_3 & not_1_out;  // AND_Gate and_1, 4 bits wide
  assign xor_3_out = X ^ Y;  // XOR_Gate xor_3, 4 bits wide
  assign or_1_out = xor_1_out | xor_2_out | xor_3_out | xor_4_out;  // OR_Gate or_1, 4 bits wide
  assign not_2_out = ~in_3;  // NOT_Gate not_2, 4 bits wide
  assign out_4 = and_1_out | and_2_out;  // OR_Gate or_2, 4 bits wide
  assign xor_4_out = X ^ Y;  // XOR_Gate xor_4, 4 bits wide
  assign and_2_out = or_1_out & not_2_out;  // AND_Gate and_2, 4 bits wide
endmodule
