// Logisim project Exemplo0034.circ as structural Verilog: 1 circuit, main circuit main
module main (
  input  [3:0] y,
  input  [3:0] x,
  input  [3:0] chave,
  output [3:0] s5,
  output [3:0] s6,
  output [3:0] s7,
  output [3:0] s8
);

  wire [3:0] nor1_out, not1_out, or1_out, xnor1_out, xor1_out;

  assign xor1_out = x ^ y;  // XOR_Gate xor1, 4 bits wide
  assign s5 = chave & xor1_out;  // AND_Gate and1, 4 bits wide
  assign xnor1_out = ~(x ^ y);  // XNOR_Gate xnor1, 4 bits wide
  assign s6 = chave & xnor1_out;  // AND_Gate and2, 4 bits wide
  assign not1_out = ~chave;  // NOT_Gate not1, 4 bits wide
  assign nor1_out = ~(x | y);  // NOR_Gate nor1, 4 bits wide
  assign s7 = not1_out & nor1_out;  // AND_Gate and3, 4 bits wide
  assign or1_out = x | y;  // OR_Gate or1, 4 bits wide
  assign s8 = not1_out & or1_out;  // AND_Gate and4, 4 bits wide

  // Notes on the sheet:
  //   chave
  //   Ederson Cristiano Nunes - 438964
  //   chave
  //   s1
  //   s5
  //   s2
  //   s6
  //   nchave
  //   nchave
  //   s3
  //   s7
  //   s4
  //   s8
endmodule
