// Logisim project Exemplo0035.circ as structural Verilog: 1 circuit, main circuit main
module main (
  input  [3:0] y,
  input  [3:0] x,
  output [3:0] s1,
  output [3:0] s3,
  output [3:0] s5,
  output [3:0] s0,
  output [3:0] s2,
  output [3:0] s4,
  output [3:0] s6,
  output [3:0] s7
);

  assign s1 = ~y;  // NOT_Gate not1, 4 bits wide
  assign s0 = ~x;  // NOT_Gate not0, 4 bits wide
  assign s2 = x | y;  // OR_Gate or0, 4 bits wide
  assign s3 = ~(y | x);  // NOR_Gate nor0, 4 bits wide
  assign s4 = x & y;  // AND_Gate and0, 4 bits wide
  assign s5 = ~(y & x);  // NAND_Gate nand0, 4 bits wide
  assign s6 = x ^ y;  // XOR_Gate xor0, 4 bits wide
  assign s7 = ~(x ^ y);  // XNOR_Gate xnor0, 4 bits wide

  // Notes on the sheet:
  //   Ederson Cristiano Nunes - 438964
endmodule
