// Logisim project AU_igual_diferente_selecionavel.circ as structural Verilog: 1 circuit, main circuit main
module main (
  input  [3:0] a,
  input  [3:0] b,
  input  in_3,
  output out_4
);

  wire and_1_out, and_2_out, and_3_out, not_1_out, not_2_out, xnor_1_out, xnor_2_out, xnor_3_out, xnor_4_out;

  xnor xnor_1 (xnor_1_out, b[0], a[0]);
  xnor xnor_2 (xnor_2_out, b[1], a[1]);
  xnor xnor_3 (xnor_3_out, b[2], a[2]);
  xnor xnor_4 (xnor_4_out, b[3], a[3]);
  and and_1 (and_1_out, xnor_1_out, xnor_2_out, xnor_3_out, xnor_4_out);
  not not_1 (not_1_out, and_1_out);
  not not_2 (not_2_out, in_3);
  and and_2 (and_2_out, and_1_out, not_2_out);
  and and_3 (and_3_out, not_1_out, in_3);
  xor xor_1 (out_4, and_2_out, and_3_out);
endmodule
