// Logisim project AU_maior_menor_selecionavel_01_bit.circ as structural Verilog: 1 circuit, main circuit main
module main (
  input  _0_maior____1_menor,
  input  a,
  input  b,
  output out_4
);

  wire and_1_out, and_2_out, and_3_out, and_4_out, not_1_out, not_2_out, not_3_out;

  not not_1 (not_1_out, b);
  not not_2 (not_2_out, a);
  and and_1 (and_1_out, a, not_1_out);
  and and_2 (and_2_out, not_2_out, b);
  and and_3 (and_3_out, and_1_out, not_3_out);
  not not_3 (not_3_out, _0_maior____1_menor);
  and and_4 (and_4_out, and_2_out, _0_maior____1_menor);
  xor xor_1 (out_4, and_3_out, and_4_out);
endmodule
