// Logisim project AU_maior_menor_selecionavel_02_bits.circ as structural Verilog: 1 circuit, main circuit main
module main (
  input  [1:0] ab,
  input  [1:0] cd,
  input  _0_maior____1_menor,
  output out_4
);

  wire and_1_out, and_2_out, and_3_out, and_4_out, and_5_out, and_6_out, and_7_out, and_8_out, not_1_out,
       not_2_out, not_3_out, not_4_out, not_5_out, or_1_out, or_2_out, or_3_out, or_4_out;

  // Probe on ab
  // Probe on cd
  not not_1 (not_1_out, cd[0]);
  not not_2 (not_2_out, cd[1]);
  not not_3 (not_3_out, ab[0]);
  not not_4 (not_4_out, ab[1]);
  and and_1 (and_1_out, ab[1], ab[0], not_1_out);
  and and_2 (and_2_out, not_3_out, cd[0]);
  and and_3 (and_3_out, not_3_out, cd[1], cd[0]);
  and and_4 (and_4_out, not_1_out, ab[0]);
  or or_1 (or_1_out, and_4_out, ab[1]);
  or or_2 (or_2_out, and_2_out, cd[1]);
  and and_5 (and_5_out, or_2_out, not_4_out);
  and and_6 (and_6_out, or_1_out, not_2_out);
  or or_3 (or_3_out, and_5_out, and_3_out);
  or or_4 (or_4_out, and_1_out, and_6_out);
  not not_5 (not_5_out, _0_maior____1_menor);
  and and_7 (and_7_out, or_4_out, not_5_out);
  and and_8 (and_8_out, or_3_out, _0_maior____1_menor);
  xor xor_1 (out_4, and_7_out, and_8_out);
endmodule
