// Logisim project LU_not_or_nor_and_nand_xor_xnor_simultaneo.circ as structural Verilog: 1 circuit, main circuit main
module main (
  input  [3:0] in_1,
  input  [3:0] in_2,
  output [3:0] out_3,
  output [3:0] out_4,
  output [3:0] out_5,
  output [3:0] out_6,
  output [3:0] out_7,
  output [3:0] out_8,
  output [3:0] out_9,
  output [3:0] out_10
);

  not not_1 (out_3[0], in_1[0]);
  not not_2 (out_3[1], in_1[1]);
  not not_3 (out_3[2], in_1[2]);
  not not_4 (out_3[3], in_1[3]);
  not not_5 (out_4[0], in_2[0]);
  not not_6 (out_4[1], in_2[1]);
  not not_7 (out_4[2], in_2[2]);
  not not_8 (out_4[3], in_2[3]);
  or or_1 (out_5[0], in_2[0], in_1[0]);
  or or_2 (out_5[1], in_2[1], in_1[1]);
  or or_3 (out_5[2], in_2[2], in_1[2]);
  or or_4 (out_5[3], in_2[3], in_1[3]);
  nor nor_1 (out_6[0], in_2[0], in_1[0]);
  nor nor_2 (out_6[1], in_2[1], in_1[1]);
  nor nor_3 (out_6[2], in_2[2], in_1[2]);
  nor nor_4 (out_6[3], in_2[3], in_1[3]);
  and and_1 (out_7[0], in_2[0], in_1[0]);
  and and_2 (out_7[1], in_2[1], in_1[1]);
  and and_3 (out_7[2], in_2[2], in_1[2]);
  and and_4 (out_7[3], in_2[3], in_1[3]);
  nand nand_1 (out_8[0], in_2[0], in_1[0]);
  nand nand_2 (out_8[1], in_2[1], in_1[1]);
  nand nand_3 (out_8[2], in_2[2], in_1[2]);
  nand nand_4 (out_8[3], in_2[3], in_1[3]);
  xor xor_1 (out_9[0], in_2[0], in_1[0]);
  xor xor_2 (out_9[1], in_2[1], in_1[1]);
  xor xor_3 (out_9[2], in_2[2], in_1[2]);
  xor xor_4 (out_9[3], in_2[3], in_1[3]);
  xnor xnor_1 (out_10[0], in_2[0], in_1[0]);
  xnor xnor_2 (out_10[1], in_2[1], in_1[1]);
  xnor xnor_3 (out_10[2], in_2[2], in_1[2]);
  xnor xnor_4 (out_10[3], in_2[3], in_1[3]);
endmodule
