// Logisim project LU_or_e_and_nor_e_nand_selecionavel.circ as structural Verilog: 2 circuits, main circuit main
module main (
  input  [3:0] in_1,
  input  [3:0] in_2,
  input  _0_OR_AND____1_NOR_NAND,
  output [3:0] out_4,
  output [3:0] out_5
);

  wire [3:0] and_1_out, nand_1_out, nor_1_out, or_1_out;

  or or_1 (or_1_out[0], in_2[0], in_1[0]);
  or or_2 (or_1_out[1], in_2[1], in_1[1]);
  or or_3 (or_1_out[2], in_2[2], in_1[2]);
  or or_4 (or_1_out[3], in_2[3], in_1[3]);
  and and_1 (and_1_out[0], in_2[0], in_1[0]);
  and and_2 (and_1_out[1], in_2[1], in_1[1]);
  and and_3 (and_1_out[2], in_2[2], in_1[2]);
  and and_4 (and_1_out[3], in_2[3], in_1[3]);
  nor nor_1 (nor_1_out[0], in_2[0], in_1[0]);
  nor nor_2 (nor_1_out[1], in_2[1], in_1[1]);
  nor nor_3 (nor_1_out[2], in_2[2], in_1[2]);
  nor nor_4 (nor_1_out[3], in_2[3], in_1[3]);
  nand nand_1 (nand_1_out[0], in_2[0], in_1[0]);
  nand nand_2 (nand_1_out[1], in_2[1], in_1[1]);
  nand nand_3 (nand_1_out[2], in_2[2], in_1[2]);
  nand nand_4 (nand_1_out[3], in_2[3], in_1[3]);
  // Probe on or_1_out
  // Probe on and_1_out
  // Probe on nor_1_out
  // Probe on nand_1_out
  chave chave_1 (
    .a___b(or_1_out), .a___b_2(and_1_out), .a_nor_b(nor_1_out), .a_nand_b(nand_1_out), .s0(out_4),
    .s1(out_5), .key(_0_OR_AND____1_NOR_NAND));
endmodule

// Chave
module chave (
  input  key,
  input  [3:0] a___b,
  input  [3:0] a___b_2,
  input  [3:0] a_nor_b,
  input  [3:0] a_nand_b,
  output [3:0] s0,
  output [3:0] s1
);

  wire [3:0] and_1_out, and_2_out, and_3_out, and_4_out, not_1_out;

  assign not_1_out = ~{4{key}};  // NOT_Gate not_1, 4 bits wide
  // Probe on and_1_out
  assign and_1_out = a___b & not_1_out;  // AND_Gate and_1, 4 bits wide
  assign and_2_out = a___b_2 & not_1_out;  // AND_Gate and_2, 4 bits wide
  // Probe on and_2_out
  // Probe on and_3_out
  assign and_3_out = a_nor_b & {4{key}};  // AND_Gate and_3, 4 bits wide
  assign and_4_out = a_nand_b & {4{key}};  // AND_Gate and_4, 4 bits wide
  // Probe on and_4_out
  assign s0 = and_1_out ^ and_3_out;  // XOR_Gate xor_1, 4 bits wide
  assign s1 = and_2_out ^ and_4_out;  // XOR_Gate xor_2, 4 bits wide

  // Notes on the sheet:
  //   sinal buffer
  //   sinal negado
  //   w0
  //   w1
  //   w2
  //   w3
endmodule
