// Logisim project LU_or_e_and_selecionavel.circ as structural Verilog: 2 circuits, main circuit main
module main (
  input  [3:0] a,
  input  [3:0] b,
  input  _0__OR____1__AND,
  output [3:0] s0
);

  wire [3:0] and_1_out, or_1_out;

  or or_1 (or_1_out[0], b[0], a[0]);
  or or_2 (or_1_out[1], b[1], a[1]);
  or or_3 (or_1_out[2], b[2], a[2]);
  or or_4 (or_1_out[3], b[3], a[3]);
  and and_1 (and_1_out[0], b[0], a[0]);
  and and_2 (and_1_out[1], b[1], a[1]);
  and and_3 (and_1_out[2], b[2], a[2]);
  and and_4 (and_1_out[3], b[3], a[3]);
  // Probe on or_1_out
  // Probe on and_1_out
  chave chave_1 (.in_2(or_1_out), .in_3(and_1_out), .chave(_0__OR____1__AND), .out_4(s0));
endmodule

// CHAVE
module chave (
  input  chave,
  input  [3:0] in_2,
  input  [3:0] in_3,
  output [3:0] out_4
);

  wire [3:0] and_1_out, and_2_out, not_1_out;

  assign and_1_out = in_2 & not_1_out;  // AND_Gate and_1, 4 bits wide
  assign not_1_out = ~{4{chave}};  // NOT_Gate not_1, 4 bits wide
  assign and_2_out = in_3 & {4{chave}};  // AND_Gate and_2, 4 bits wide
  // Probe on and_1_out
  // Probe on and_2_out
  assign out_4 = and_1_out ^ and_2_out;  // XOR_Gate xor_1, 4 bits wide
endmodule
