// Logisim project LU_or_e_and_simultaneo.circ as structural Verilog: 1 circuit, main circuit main
module main (
  input  [3:0] a,
  input  [3:0] b,
  output [3:0] a_and_b,
  output [3:0] a_or_b
);

  and and_1 (a_and_b[3], a[3], b[3]);
  and and_2 (a_and_b[2], a[2], b[2]);
  and and_3 (a_and_b[1], a[1], b[1]);
  and and_4 (a_and_b[0], a[0], b[0]);
  or or_1 (a_or_b[3], a[3], b[3]);
  or or_2 (a_or_b[2], a[2], b[2]);
  or or_3 (a_or_b[1], a[1], b[1]);
  or or_4 (a_or_b[0], a[0], b[0]);
endmodule
