// Logisim project LU_or_e_nor_xor_e_xnor_selecionavel.circ as structural Verilog: 2 circuits, main circuit main
module main (
  input  [3:0] in_1,
  input  [3:0] in_2,
  input  _0_OR_NOR____1_XOR_XNOR,
  output [3:0] out_4,
  output [3:0] out_5
);

  wire [3:0] nor_1_out, or_1_out, xnor_1_out, xor_1_out;

  or or_1 (or_1_out[0], in_2[0], in_1[0]);
  or or_2 (or_1_out[1], in_2[1], in_1[1]);
  or or_3 (or_1_out[2], in_2[2], in_1[2]);
  or or_4 (or_1_out[3], in_2[3], in_1[3]);
  nor nor_1 (nor_1_out[0], in_2[0], in_1[0]);
  nor nor_2 (nor_1_out[1], in_2[1], in_1[1]);
  nor nor_3 (nor_1_out[2], in_2[2], in_1[2]);
  nor nor_4 (nor_1_out[3], in_2[3], in_1[3]);
  xor xor_1 (xor_1_out[0], in_2[0], in_1[0]);
  xor xor_2 (xor_1_out[1], in_2[1], in_1[1]);
  xor xor_3 (xor_1_out[2], in_2[2], in_1[2]);
  xor xor_4 (xor_1_out[3], in_2[3], in_1[3]);
  xnor xnor_1 (xnor_1_out[0], in_2[0], in_1[0]);
  xnor xnor_2 (xnor_1_out[1], in_2[1], in_1[1]);
  xnor xnor_3 (xnor_1_out[2], in_2[2], in_1[2]);
  xnor xnor_4 (xnor_1_out[3], in_2[3], in_1[3]);
  // Probe on or_1_out
  // Probe on nor_1_out
  // Probe on xor_1_out
  // Probe on xnor_1_out
  chave chave_1 (
    .a___b(or_1_out), .a___b_2(nor_1_out), .a_nor_b(xor_1_out), .a_nand_b(xnor_1_out), .s0(out_4),
    .s1(out_5), .key(_0_OR_NOR____1_XOR_XNOR));
endmodule

// Chave
module chave (
  input  key,
  input  [3:0] a___b,
  input  [3:0] a___b_2,
  input  [3:0] a_nor_b,
  input  [3:0] a_nand_b,
  output [3:0] s0,
  output [3:0] s1
);

  wire [3:0] and_1_out, and_2_out, and_3_out, and_4_out, not_1_out;

  assign not_1_out = ~{4{key}};  // NOT_Gate not_1, 4 bits wide
  // Probe on and_1_out
  assign and_1_out = a___b & not_1_out;  // AND_Gate and_1, 4 bits wide
  assign and_2_out = a___b_2 & not_1_out;  // AND_Gate and_2, 4 bits wide
  // Probe on and_2_out
  // Probe on and_3_out
  assign and_3_out = a_nor_b & {4{key}};  // AND_Gate and_3, 4 bits wide
  assign and_4_out = a_nand_b & {4{key}};  // AND_Gate and_4, 4 bits wide
  // Probe on and_4_out
  assign s0 = and_1_out ^ and_3_out;  // XOR_Gate xor_1, 4 bits wide
  assign s1 = and_2_out ^ and_4_out;  // XOR_Gate xor_2, 4 bits wide

  // Notes on the sheet:
  //   sinal buffer
  //   sinal negado
  //   w0
  //   w1
  //   w2
  //   w3
endmodule
