// Logisim project Complemento de 2.circ as structural Verilog: 1 circuit, main circuit complemento de 2
module complemento_de_2 (
  input  in_1,
  input  [5:0] in_2,
  output [5:0] out_3,
  output out_4
);

  wire [5:0] not_1_out;

  assign not_1_out = ~in_2;  // NOT_Gate not_1, 6 bits wide
  Adder #(.width(6)) adder_1 (.a(not_1_out), .b({6{1'b0}}), .out(out_3), .cin(in_1), .cout(out_4));
endmodule
