// Logisim project Somador 6 bits.circ as structural Verilog: 3 circuits, main circuit Somador 6 bits
module Somador_6_bits (
  input  in_1,
  input  in_2,
  input  in_3,
  input  in_4,
  input  in_5,
  input  in_6,
  input  in_7,
  input  in_8,
  input  in_9,
  input  in_10,
  input  in_11,
  input  in_12,
  input  in_13,
  output out_14,
  output [5:0] out_15
);

  wire soma_completa_2_out_5, soma_completa_3_out_5, soma_completa_4_out_5, soma_completa_5_out_5,
       soma_completa_6_out_5;

  soma_completa soma_completa_1 (
    .in_1(soma_completa_2_out_5), .in_2(in_6), .in_3(in_13), .out_4(out_15[5]), .out_5(out_14));
  soma_completa soma_completa_2 (
    .in_1(soma_completa_4_out_5), .in_2(in_5), .in_3(in_12), .out_4(out_15[4]), .out_5(soma_completa_2_out_5));
  soma_completa soma_completa_3 (
    .in_1(soma_completa_5_out_5), .in_2(in_3), .in_3(in_9), .out_4(out_15[2]), .out_5(soma_completa_3_out_5));
  soma_completa soma_completa_4 (
    .in_1(soma_completa_3_out_5), .in_2(in_4), .in_3(in_11), .out_4(out_15[3]), .out_5(soma_completa_4_out_5));
  soma_completa soma_completa_5 (
    .in_1(soma_completa_6_out_5), .in_2(in_2), .in_3(in_8), .out_4(out_15[1]), .out_5(soma_completa_5_out_5));
  soma_completa soma_completa_6 (
    .in_1(in_10), .in_2(in_1), .in_3(in_7), .out_4(out_15[0]), .out_5(soma_completa_6_out_5));
endmodule

module meiaSoma (
  input  in_1,
  input  in_2,
  output out_3,
  output out_4
);

  xor xor_1 (out_3, in_1, in_2);
  and and_1 (out_4, in_1, in_2);
endmodule

module soma_completa (
  input  in_1,
  input  in_2,
  input  in_3,
  output out_4,
  output out_5
);

  wire meiasoma_1_out_3, meiasoma_1_out_4, meiasoma_2_out_4;

  meiaSoma meiasoma_1 (.in_1(in_2), .in_2(in_3), .out_3(meiasoma_1_out_3), .out_4(meiasoma_1_out_4));
  meiaSoma meiasoma_2 (.in_1(in_1), .in_2(meiasoma_1_out_3), .out_3(out_4), .out_4(meiasoma_2_out_4));
  or or_1 (out_5, meiasoma_2_out_4, meiasoma_1_out_4);
endmodule
