// Logisim project Subtrator 6 bits.circ as structural Verilog: 3 circuits, main circuit meiaSub
module meiaSub (
  input  in_1,
  input  in_2,
  output out_3,
  output out_4
);

  wire not_1_out;

  not not_1 (not_1_out, in_2);
  xor xor_1 (out_3, in_1, in_2);
  and and_1 (out_4, in_1, not_1_out);
endmodule

module Sub_completa (
  input  in_1,
  input  in_2,
  input  in_3,
  output out_4,
  output out_5
);

  wire and_1_out, meiasub_1_out_3, meiasub_1_out_4, not_1_out;

  meiaSub meiasub_1 (.in_1(in_2), .in_2(in_3), .out_3(meiasub_1_out_3), .out_4(meiasub_1_out_4));
  xor xor_1 (out_4, in_1, meiasub_1_out_3);
  not not_1 (not_1_out, meiasub_1_out_3);
  and and_1 (and_1_out, in_1, not_1_out);
  or or_1 (out_5, and_1_out, meiasub_1_out_4);
endmodule

module Sub_6_bits (
  input  [5:0] A,
  input  [5:0] B,
  input  in_3,
  output out_4,
  output [5:0] out_5
);

  wire sub_completa_2_out_5, sub_completa_3_out_5, sub_completa_4_out_5, sub_completa_5_out_5,
       sub_completa_6_out_5;

  Sub_completa sub_completa_1 (.in_1(sub_completa_2_out_5), .in_2(B[5]), .in_3(A[5]), .out_4(out_5[5]), .out_5(out_4));
  Sub_completa sub_completa_2 (
    .in_1(sub_completa_3_out_5), .in_2(B[4]), .in_3(A[4]), .out_4(out_5[4]), .out_5(sub_completa_2_out_5));
  Sub_completa sub_completa_3 (
    .in_1(sub_completa_4_out_5), .in_2(B[3]), .in_3(A[3]), .out_4(out_5[3]), .out_5(sub_completa_3_out_5));
  Sub_completa sub_completa_4 (
    .in_1(sub_completa_5_out_5), .in_2(B[2]), .in_3(A[2]), .out_4(out_5[2]), .out_5(sub_completa_4_out_5));
  Sub_completa sub_completa_5 (
    .in_1(sub_completa_6_out_5), .in_2(B[1]), .in_3(A[1]), .out_4(out_5[1]), .out_5(sub_completa_5_out_5));
  Sub_completa sub_completa_6 (.in_1(in_3), .in_2(B[0]), .in_3(A[0]), .out_4(out_5[0]), .out_5(sub_completa_6_out_5));
endmodule
