// Logisim project guia04.circ as structural Verilog
// HA
module HALF_ADDER_2BITS (
  input  Y,
  input  X,
  output S,
  output C_OUT
);

  xor xor_1 (S, Y, X);
  and and_1 (C_OUT, Y, X);

  // Notes on the sheet:
  //   HALF ADDER 2 BITS
endmodule

// FA
module FULL_ADDER_2BITS (
  input  C_IN,
  input  Y,
  input  X,
  output S,
  output C_OUT
);

  wire half_adder_2bits_1_c_out, half_adder_2bits_1_s, half_adder_2bits_2_c_out;

  HALF_ADDER_2BITS half_adder_2bits_1 (.Y(Y), .X(X), .C_OUT(half_adder_2bits_1_c_out), .S(half_adder_2bits_1_s));
  HALF_ADDER_2BITS half_adder_2bits_2 (.Y(C_IN), .X(half_adder_2bits_1_s), .C_OUT(half_adder_2bits_2_c_out), .S(S));
  or or_1 (C_OUT, half_adder_2bits_2_c_out, half_adder_2bits_1_c_out);

  // Notes on the sheet:
  //   FULL ADDER 2 BITS
endmodule

module Exercicio0021 (
  input  Sinal_A,
  input  Sinal_B,
  input  A4,
  input  B4,
  input  A3,
  input  B3,
  input  A2,
  input  B2,
  input  A1,
  input  B1,
  input  A0,
  input  B0,
  output S_Sinal,
  output S4,
  output S3,
  output S2,
  output S1,
  output S0
);

  wire full_adder_2bits_1_c_out, full_adder_2bits_2_c_out, full_adder_2bits_3_c_out,
       full_adder_2bits_4_c_out, half_adder_2bits_1_c_out;

  FULL_ADDER_2BITS full_adder_2bits_1 (
    .Y(A4), .X(B4), .C_IN(full_adder_2bits_2_c_out), .S(S4), .C_OUT(full_adder_2bits_1_c_out));
  FULL_ADDER_2BITS full_adder_2bits_2 (
    .Y(A3), .X(B3), .C_IN(full_adder_2bits_3_c_out), .S(S3), .C_OUT(full_adder_2bits_2_c_out));
  FULL_ADDER_2BITS full_adder_2bits_3 (
    .Y(A2), .X(B2), .C_IN(full_adder_2bits_4_c_out), .S(S2), .C_OUT(full_adder_2bits_3_c_out));
  FULL_ADDER_2BITS full_adder_2bits_4 (
    .Y(A1), .X(B1), .C_IN(half_adder_2bits_1_c_out), .S(S1), .C_OUT(full_adder_2bits_4_c_out));
  HALF_ADDER_2BITS half_adder_2bits_1 (.Y(A0), .X(B0), .C_OUT(half_adder_2bits_1_c_out), .S(S0));
  FULL_ADDER_2BITS full_adder_2bits_5 (
    .Y(Sinal_A), .X(Sinal_B), .C_IN(full_adder_2bits_1_c_out), .S(S_Sinal));  // open: C_OUT

  // Notes on the sheet:
  //   A soma com sinal de numeros binarios occore de forma normal a uma soma
  //   sem sinal, cada bit é somando com seu correspondente e com o carry out
  //   anterior, mas no final, na soma dos sinais, o carry_out que sair dele é ignorado
  //   Ex:
  //   1 01101
  //   +
  //   0 10011
  //   ___________
  //   0 00000
  //   -19
  //   19
  //   0
  //   +
  //   -20
  //   1 01100
  //   19
  //   0 10011
  //   ___________
  //   -1
  //   1 11111
endmodule

// HS
module HALF_SUBTRACTOR_2BITS (
  input  A,
  input  B,
  output S,
  output B_OUT
);

  wire not_1_out;

  xor xor_1 (S, B, A);
  not not_1 (not_1_out, A);
  and and_1 (B_OUT, B, not_1_out);

  // Notes on the sheet:
  //   HALF SUBTRACTOR 2 BITS
endmodule

// FS
module FULL_SUBTRACTOR_2BITS (
  input  X,
  input  Y,
  input  B_IN,
  output S,
  output B_OUT
);

  wire half_subtractor_2bits_1_b_out, half_subtractor_2bits_1_s, half_subtractor_2bits_2_b_out;

  HALF_SUBTRACTOR_2BITS half_subtractor_2bits_1 (
    .A(X), .B(Y), .B_OUT(half_subtractor_2bits_1_b_out), .S(half_subtractor_2bits_1_s));
  HALF_SUBTRACTOR_2BITS half_subtractor_2bits_2 (
    .A(half_subtractor_2bits_1_s), .B(B_IN), .B_OUT(half_subtractor_2bits_2_b_out), .S(S));
  or or_1 (B_OUT, half_subtractor_2bits_2_b_out, half_subtractor_2bits_1_b_out);

  // Notes on the sheet:
  //   FULL SUBTRACTOR 2 BITS
endmodule

module Exemplo0022 (
  input  B0,
  input  A0,
  input  B1,
  input  A1,
  input  B2,
  input  A2,
  input  B3,
  input  A3,
  input  B4,
  input  A4,
  input  Sinal_B,
  input  Sinal_A,
  output S0,
  output S1,
  output S2,
  output S3,
  output S4,
  output S_Sinal
);

  wire full_subtractor_2bits_2_b_out, full_subtractor_2bits_3_b_out, full_subtractor_2bits_4_b_out,
       full_subtractor_2bits_5_b_out, half_subtractor_2bits_1_b_out;

  FULL_SUBTRACTOR_2BITS full_subtractor_2bits_1 (
    .X(full_subtractor_2bits_2_b_out), .Y(Sinal_A), .B_IN(Sinal_B), .S(S_Sinal));  // open: B_OUT
  FULL_SUBTRACTOR_2BITS full_subtractor_2bits_2 (
    .X(full_subtractor_2bits_4_b_out), .Y(A4), .B_IN(B4), .S(S4), .B_OUT(full_subtractor_2bits_2_b_out));
  FULL_SUBTRACTOR_2BITS full_subtractor_2bits_3 (
    .X(full_subtractor_2bits_5_b_out), .Y(A2), .B_IN(B2), .S(S2), .B_OUT(full_subtractor_2bits_3_b_out));
  FULL_SUBTRACTOR_2BITS full_subtractor_2bits_4 (
    .X(full_subtractor_2bits_3_b_out), .Y(A3), .B_IN(B3), .S(S3), .B_OUT(full_subtractor_2bits_4_b_out));
  FULL_SUBTRACTOR_2BITS full_subtractor_2bits_5 (
    .X(half_subtractor_2bits_1_b_out), .Y(A1), .B_IN(B1), .S(S1), .B_OUT(full_subtractor_2bits_5_b_out));
  HALF_SUBTRACTOR_2BITS half_subtractor_2bits_1 (.A(A0), .B(B0), .B_OUT(half_subtractor_2bits_1_b_out), .S(S0));

  // Notes on the sheet:
  //   1 10101
  //   -
  //   0 01011
  //   ___________
  //   1 01010
  //   A lógica do subtrador segue a mesma do somador
endmodule

// ==
module EQUALS_2BITS (
  input  P,
  input  Q,
  output S
);

  xnor xnor_1 (S, P, Q);
endmodule

module Exemplo0023 (
  input  Sinal_P,
  input  P4,
  input  P3,
  input  P2,
  input  P1,
  input  P0,
  input  Sinal_P_2,
  input  P4_2,
  input  P3_2,
  input  P2_2,
  input  P1_2,
  input  P0_2,
  output S
);

  wire equals_2bits_1_s, equals_2bits_2_s, equals_2bits_3_s, equals_2bits_4_s, equals_2bits_5_s,
       equals_2bits_6_s;

  EQUALS_2BITS equals_2bits_1 (.P(Sinal_P), .Q(Sinal_P_2), .S(equals_2bits_1_s));
  EQUALS_2BITS equals_2bits_2 (.P(P4), .Q(P4_2), .S(equals_2bits_2_s));
  EQUALS_2BITS equals_2bits_3 (.P(P3), .Q(P3_2), .S(equals_2bits_3_s));
  EQUALS_2BITS equals_2bits_4 (.P(P2), .Q(P2_2), .S(equals_2bits_4_s));
  EQUALS_2BITS equals_2bits_5 (.P(P1), .Q(P1_2), .S(equals_2bits_5_s));
  EQUALS_2BITS equals_2bits_6 (.P(P0), .Q(P0_2), .S(equals_2bits_6_s));
  and and_1 (S, equals_2bits_1_s, equals_2bits_2_s, equals_2bits_3_s, equals_2bits_4_s, equals_2bits_5_s, equals_2bits_6_s);

  // Notes on the sheet:
  //   Comparador de igualdade 6 BITS
endmodule

// !=
module DIFERENT_2BITS (
  input  P,
  input  Q,
  output S
);

  xor xor_1 (S, P, Q);
endmodule

module Exemplo0024 (
  input  Sinal_P,
  input  P4,
  input  P3,
  input  P2,
  input  P1,
  input  P0,
  input  Sinal_P_2,
  input  P4_2,
  input  P3_2,
  input  P2_2,
  input  P1_2,
  input  P0_2,
  output S
);

  wire diferent_2bits_1_s, diferent_2bits_2_s, diferent_2bits_3_s, diferent_2bits_4_s, diferent_2bits_5_s,
       diferent_2bits_6_s;

  DIFERENT_2BITS diferent_2bits_1 (.P(Sinal_P), .Q(Sinal_P_2), .S(diferent_2bits_1_s));
  DIFERENT_2BITS diferent_2bits_2 (.P(P4), .Q(P4_2), .S(diferent_2bits_2_s));
  DIFERENT_2BITS diferent_2bits_3 (.P(P3), .Q(P3_2), .S(diferent_2bits_3_s));
  DIFERENT_2BITS diferent_2bits_4 (.P(P2), .Q(P2_2), .S(diferent_2bits_4_s));
  DIFERENT_2BITS diferent_2bits_5 (.P(P1), .Q(P1_2), .S(diferent_2bits_5_s));
  DIFERENT_2BITS diferent_2bits_6 (.P(P0), .Q(P0_2), .S(diferent_2bits_6_s));
  or or_1 (S, diferent_2bits_1_s, diferent_2bits_2_s, diferent_2bits_3_s, diferent_2bits_4_s, diferent_2bits_5_s, diferent_2bits_6_s);

  // Notes on the sheet:
  //   Comparador de diferença 6 BITS
endmodule

module Exemplo0025 (
  input  plus_1,
  input  Sinal_P,
  input  P4,
  input  P3,
  input  P2,
  input  P1,
  input  P0,
  output S0,
  output S1,
  output S2,
  output S3,
  output S4,
  output Sinal
);

  wire half_adder_2bits_2_c_out, half_adder_2bits_3_c_out, half_adder_2bits_4_c_out,
       half_adder_2bits_5_c_out, half_adder_2bits_6_c_out, not_1_out, not_2_out, not_3_out, not_4_out,
       not_5_out, not_6_out;

  not not_1 (not_1_out, Sinal_P);
  HALF_ADDER_2BITS half_adder_2bits_1 (.Y(half_adder_2bits_3_c_out), .X(not_1_out), .S(Sinal));  // open: C_OUT
  not not_2 (not_2_out, P4);
  not not_3 (not_3_out, P3);
  HALF_ADDER_2BITS half_adder_2bits_2 (
    .Y(half_adder_2bits_5_c_out), .X(not_3_out), .C_OUT(half_adder_2bits_2_c_out), .S(S3));
  HALF_ADDER_2BITS half_adder_2bits_3 (
    .Y(half_adder_2bits_2_c_out), .X(not_2_out), .C_OUT(half_adder_2bits_3_c_out), .S(S4));
  not not_4 (not_4_out, P2);
  not not_5 (not_5_out, P1);
  HALF_ADDER_2BITS half_adder_2bits_4 (
    .Y(half_adder_2bits_6_c_out), .X(not_5_out), .C_OUT(half_adder_2bits_4_c_out), .S(S1));
  HALF_ADDER_2BITS half_adder_2bits_5 (
    .Y(half_adder_2bits_4_c_out), .X(not_4_out), .C_OUT(half_adder_2bits_5_c_out), .S(S2));
  not not_6 (not_6_out, P0);
  HALF_ADDER_2BITS half_adder_2bits_6 (.Y(plus_1), .X(not_6_out), .C_OUT(half_adder_2bits_6_c_out), .S(S0));

  // Notes on the sheet:
  //   senão será feito Complemento de 1
  //   Deixar essa entrada em 1 para fazer Complemento de 2 da entrada,
endmodule

module FULL_ADDER_SUB_2BITS_Extra (
  input  OP,
  input  Y,
  input  X,
  output S,
  output C_OUT
);

  wire full_adder_2bits_1_c_out, xor_1_out;

  xor xor_1 (xor_1_out, OP, Y);
  FULL_ADDER_2BITS full_adder_2bits_1 (.Y(xor_1_out), .X(X), .C_IN(OP), .S(S), .C_OUT(full_adder_2bits_1_c_out));
  xor xor_2 (C_OUT, full_adder_2bits_1_c_out, Y);

  // Notes on the sheet:
  //   A função da porta XOR é definir a operção:
  //   se a porta XOR = 0, teremos a soma; se XOR = ,1teremos a subtração
  //   com isso o circuito FULL ADDER fará a soma das entradas;
  //   FULL ADDER COM ESOCLHA DE OPERAÇÃO ( + OU - ) DE ACORDO COM OP
  //   mas quando temos o sinal da XOR igual a 1 temos a inversão do outro sinal na saida
  //   isso ocorre pois quando um dos sinais da XOR é 0 temos a cópia do outro sinal na saida
  //   então o FULL ADDER fará a soma das entradas, mas com uma delas invertidas, com isso temos a subtração
endmodule
