// Logisim project Exemplo0021.v.circ as structural Verilog: 4 circuits, main circuit main
module main (
  input  [4:0] in_1,
  input  [4:0] in_2,
  input  in_3,
  output [5:0] out_4
);

  wire somaparalelo_2_vai_um_2, somaparalelo_3_vai_um_2, somaparalelo_4_vai_um_2, somaparalelo_5_vai_um_2;

  SomaParalelo somaparalelo_1 (
    .Vai_um_2(out_4[5]), .vai_um(somaparalelo_3_vai_um_2), .s0(out_4[4]), .y(in_1[4]), .x(in_2[4]));
  SomaParalelo somaparalelo_2 (
    .Vai_um_2(somaparalelo_2_vai_um_2), .vai_um(somaparalelo_4_vai_um_2), .s0(out_4[2]), .y(in_1[2]),
    .x(in_2[2]));
  SomaParalelo somaparalelo_3 (
    .Vai_um_2(somaparalelo_3_vai_um_2), .vai_um(somaparalelo_2_vai_um_2), .s0(out_4[3]), .y(in_1[3]),
    .x(in_2[3]));
  SomaParalelo somaparalelo_4 (
    .Vai_um_2(somaparalelo_4_vai_um_2), .vai_um(somaparalelo_5_vai_um_2), .s0(out_4[1]), .y(in_1[1]),
    .x(in_2[1]));
  SomaParalelo somaparalelo_5 (
    .Vai_um_2(somaparalelo_5_vai_um_2), .vai_um(in_3), .s0(out_4[0]), .y(in_1[0]), .x(in_2[0]));
endmodule

module MS (
  input  in_1,
  input  in_2,
  output out_3,
  output out_4
);

  xor xor_1 (out_3, in_1, in_2);
  and and_1 (out_4, in_2, in_1);
endmodule

module SC (
  input  Vai_um,
  input  y,
  input  x,
  output s1,
  output s2
);

  wire ms_1_out_3, ms_1_out_4, ms_2_out_4;

  MS ms_1 (.in_1(y), .in_2(x), .out_3(ms_1_out_3), .out_4(ms_1_out_4));
  MS ms_2 (.in_1(Vai_um), .in_2(ms_1_out_3), .out_3(s2), .out_4(ms_2_out_4));
  or or_1 (s1, ms_2_out_4, ms_1_out_4);
endmodule

module SomaParalelo (
  input  y,
  input  x,
  input  vai_um,
  output Vai_um_2,
  output s0
);

  SC sc_1 (.Vai_um(vai_um), .y(x), .x(y), .s1(Vai_um_2), .s2(s0));
endmodule
