// Logisim project Exemplo0021.circ as structural Verilog: 1 circuit, main circuit main
module main (
  input  a,
  input  b,
  output c,
  output s
);

  xor s1 (s, a, b);
  and s2 (c, a, b);
endmodule
