// Logisim project Exemplo0022.circ as structural Verilog: 1 circuit, main circuit main
module main (
  input  Bin,
  input  a,
  input  b,
  output Di,
  output Bout
);

  wire not_1_out, not_2_out, s2_out, s3_out, s4_out;

  xor s4 (s4_out, a, b);
  not not_1 (not_1_out, a);
  not not_2 (not_2_out, s4_out);
  and s3 (s3_out, not_1_out, b);
  xor s1 (Di, Bin, s4_out);
  and s2 (s2_out, not_2_out, Bin);
  or s0 (Bout, s2_out, s3_out);

  // Notes on the sheet:
  //   Full Subtract
endmodule
