// Logisim project Exemplo0023.circ as structural Verilog: 1 circuit, main circuit main
module main (
  input  a,
  input  b,
  output a___b
);

  xnor xnor_1 (a___b, a, b);

  // Notes on the sheet:
  //   Comparador Igualdade
endmodule
