// Logisim project Exemplo0024.circ as structural Verilog: 1 circuit, main circuit main
module main (
  input  a,
  input  b,
  output a____b
);

  xor xor_1 (a____b, a, b);

  // Notes on the sheet:
  //   Comparador Diferença
endmodule
