// Logisim project guia4.circ as structural Verilog: 10 circuits, main circuit MeiaSoma
// MS
module MeiaSoma (
  input  a,
  input  b,
  output s0,
  output s1
);

  xor xor_1 (s0, b, a);
  and and_1 (s1, b, a);
endmodule

// SC
module SomaCompleta (
  input  carryIn,
  input  a,
  input  b,
  output s1,
  output s0
);

  wire meiasoma_1_s0, meiasoma_1_s1, meiasoma_2_s1;

  MeiaSoma meiasoma_1 (.a(a), .b(b), .s0(meiasoma_1_s0), .s1(meiasoma_1_s1));
  MeiaSoma meiasoma_2 (.a(meiasoma_1_s0), .b(carryIn), .s0(s0), .s1(meiasoma_2_s1));
  or or_1 (s1, meiasoma_2_s1, meiasoma_1_s1);
endmodule

module Exemplo0021 (
  input  in_1,
  input  in_2,
  input  in_3,
  input  in_4,
  input  in_5,
  input  in_6,
  input  in_7,
  input  in_8,
  input  in_9,
  input  in_10,
  input  in_11,
  input  in_12,
  output out_13,
  output out_14,
  output out_15,
  output out_16,
  output out_17,
  output out_18
);

  wire meiasoma_1_s1, somacompleta_2_s1, somacompleta_3_s1, somacompleta_4_s1, somacompleta_5_s1;

  SomaCompleta somacompleta_1 (.a(in_1), .b(in_7), .carryIn(somacompleta_2_s1), .s0(out_13));  // open: s1
  SomaCompleta somacompleta_2 (.a(in_2), .b(somacompleta_5_s1), .carryIn(in_8), .s1(somacompleta_2_s1), .s0(out_14));
  MeiaSoma meiasoma_1 (.a(in_6), .b(in_12), .s0(out_18), .s1(meiasoma_1_s1));
  SomaCompleta somacompleta_3 (.a(in_5), .b(in_11), .carryIn(meiasoma_1_s1), .s1(somacompleta_3_s1), .s0(out_17));
  SomaCompleta somacompleta_4 (.a(in_4), .b(in_10), .carryIn(somacompleta_3_s1), .s1(somacompleta_4_s1), .s0(out_16));
  SomaCompleta somacompleta_5 (.a(in_3), .b(in_9), .carryIn(somacompleta_4_s1), .s1(somacompleta_5_s1), .s0(out_15));
endmodule

// MS
module MeiaSubtracao (
  input  a,
  input  b,
  output s0,
  output s1
);

  wire not_1_out;

  not not_1 (not_1_out, a);
  xor xor_1 (s0, a, b);
  and and_1 (s1, not_1_out, b);
endmodule

module SubtracaoCompleta (
  input  a,
  input  b,
  input  Bin,
  output s0,
  output s1
);

  wire meiasubtracao_1_s0, meiasubtracao_1_s1, meiasubtracao_2_s1;

  MeiaSubtracao meiasubtracao_1 (.a(a), .b(b), .s0(meiasubtracao_1_s0), .s1(meiasubtracao_1_s1));
  MeiaSubtracao meiasubtracao_2 (.a(meiasubtracao_1_s0), .b(Bin), .s0(s0), .s1(meiasubtracao_2_s1));
  or or_1 (s1, meiasubtracao_2_s1, meiasubtracao_1_s1);
endmodule

// Soma 6-bits
module Exemplo0022 (
  input  in_1,
  input  in_2,
  input  in_3,
  input  in_4,
  input  in_5,
  input  in_6,
  input  in_7,
  input  in_8,
  input  in_9,
  input  in_10,
  input  in_11,
  input  in_12,
  output out_13,
  output out_14,
  output out_15,
  output out_16,
  output out_17,
  output out_18
);

  wire meiasubtracao_1_s1, subtracaocompleta_1_s1, subtracaocompleta_2_s1, subtracaocompleta_3_s1,
       subtracaocompleta_4_s1;

  MeiaSubtracao meiasubtracao_1 (.a(in_6), .b(in_12), .s0(out_18), .s1(meiasubtracao_1_s1));
  SubtracaoCompleta subtracaocompleta_1 (
    .a(in_5), .b(in_11), .Bin(meiasubtracao_1_s1), .s1(subtracaocompleta_1_s1), .s0(out_17));
  SubtracaoCompleta subtracaocompleta_2 (
    .a(in_4), .b(in_10), .Bin(subtracaocompleta_1_s1), .s1(subtracaocompleta_2_s1), .s0(out_16));
  SubtracaoCompleta subtracaocompleta_3 (
    .a(in_3), .b(in_9), .Bin(subtracaocompleta_2_s1), .s1(subtracaocompleta_3_s1), .s0(out_15));
  SubtracaoCompleta subtracaocompleta_4 (
    .a(in_2), .b(in_8), .Bin(subtracaocompleta_3_s1), .s1(subtracaocompleta_4_s1), .s0(out_14));
  SubtracaoCompleta subtracaocompleta_5 (.a(in_1), .b(in_7), .Bin(subtracaocompleta_4_s1), .s0(out_13));  // open: s1
endmodule

module Exemplo0023 (
  input  a0,
  input  b0,
  input  a1,
  input  b1,
  input  a2,
  input  b2,
  input  a3,
  input  b3,
  input  a4,
  input  b4,
  input  a5,
  input  b5,
  output out_13
);

  wire and_1_out, and_2_out, and_3_out, and_4_out, xnor_1_out, xnor_2_out, xnor_3_out, xnor_4_out,
       xnor_5_out, xnor_6_out;

  xnor xnor_1 (xnor_1_out, a0, b0);
  xnor xnor_2 (xnor_2_out, a1, b1);
  xnor xnor_3 (xnor_3_out, a2, b2);
  xnor xnor_4 (xnor_4_out, a3, b3);
  xnor xnor_5 (xnor_5_out, a4, b4);
  xnor xnor_6 (xnor_6_out, a5, b5);
  and and_1 (and_1_out, xnor_1_out, xnor_2_out);
  and and_2 (and_2_out, xnor_3_out, xnor_4_out);
  and and_3 (and_3_out, xnor_5_out, xnor_6_out);
  and and_4 (and_4_out, and_2_out, and_3_out);
  and and_5 (out_13, and_1_out, and_4_out);
endmodule

module Exemplo0024 (
  input  a0,
  input  b0,
  input  a1,
  input  b1,
  input  a2,
  input  b2,
  input  a3,
  input  b3,
  input  a4,
  input  b4,
  input  a5,
  input  b5,
  input  a6,
  input  b6,
  output out_15
);

  wire or_1_out, or_2_out, or_3_out, or_4_out, or_5_out, xor_1_out, xor_2_out, xor_3_out, xor_4_out,
       xor_5_out, xor_6_out, xor_7_out;

  xor xor_1 (xor_1_out, a0, b0);
  xor xor_2 (xor_2_out, a1, b1);
  xor xor_3 (xor_3_out, a2, b2);
  xor xor_4 (xor_4_out, a3, b3);
  xor xor_5 (xor_5_out, a4, b4);
  xor xor_6 (xor_6_out, a5, b5);
  xor xor_7 (xor_7_out, a6, b6);
  or or_1 (or_1_out, xor_1_out, xor_2_out);
  or or_2 (or_2_out, xor_3_out, xor_4_out);
  or or_3 (or_3_out, xor_5_out, xor_6_out);
  or or_4 (or_4_out, or_3_out, xor_7_out);
  or or_5 (or_5_out, or_2_out, or_4_out);
  or or_6 (out_15, or_1_out, or_5_out);
endmodule

module Exenplo0025 (
  input  in_1,
  input  in_2,
  input  in_3,
  input  in_4,
  input  in_5,
  input  in_6,
  input  in_7,
  input  in_8,
  input  in_9,
  input  in_10,
  input  in_11,
  input  in_12,
  output out_13,
  output out_14,
  output out_15,
  output out_16,
  output out_17,
  output out_18
);

  wire complemento_de_1_1_out_7, complemento_de_1_1_out_8, complemento_de_1_1_out_9,
       complemento_de_1_1_out_10, complemento_de_1_1_out_11, complemento_de_1_1_out_12;

  Complemento_de_1 complemento_de_1_1 (
    .in_1(in_1), .in_2(in_2), .in_3(in_3), .in_4(in_4), .in_5(in_5), .in_6(in_6),
    .out_7(complemento_de_1_1_out_7), .out_8(complemento_de_1_1_out_8), .out_9(complemento_de_1_1_out_9),
    .out_10(complemento_de_1_1_out_10), .out_11(complemento_de_1_1_out_11), .out_12(complemento_de_1_1_out_12));
  Exemplo0021 exemplo0021_1 (
    .in_1(complemento_de_1_1_out_7), .in_2(complemento_de_1_1_out_8), .in_3(complemento_de_1_1_out_9),
    .in_4(complemento_de_1_1_out_10), .in_5(complemento_de_1_1_out_11), .in_6(complemento_de_1_1_out_12),
    .in_7(in_7), .in_8(in_8), .in_9(in_9), .in_10(in_10), .in_11(in_11), .in_12(in_12), .out_13(out_13),
    .out_14(out_14), .out_15(out_15), .out_16(out_16), .out_17(out_17), .out_18(out_18));
endmodule

// C1
module Complemento_de_1 (
  input  in_1,
  input  in_2,
  input  in_3,
  input  in_4,
  input  in_5,
  input  in_6,
  output out_7,
  output out_8,
  output out_9,
  output out_10,
  output out_11,
  output out_12
);

  not not_1 (out_7, in_1);
  not not_2 (out_9, in_3);
  not not_3 (out_11, in_5);
  not not_4 (out_10, in_4);
  not not_5 (out_8, in_2);
  not not_6 (out_12, in_6);
endmodule
