// Logisim project Exemplo0041.circ as structural Verilog: 1 circuit, main circuit main
module main (
  input  carry_in,
  input  [5:0] x,
  input  [5:0] y,
  output [5:0] soma,
  output carry_out
);

  Adder #(.width(6)) adder_1 (.a(x), .b(y), .out(soma), .cin(carry_in), .cout(carry_out));

  // Notes on the sheet:
  //   Mateus Augusto Moraes Ferreira    Matricula: 435669
  //   somador
endmodule
