// Logisim project Exemplo0042.circ as structural Verilog: 1 circuit, main circuit main
module main (
  input  in_1,
  input  [5:0] x,
  input  [5:0] y,
  output [5:0] out_4
);

  Subtractor #(.width(6)) subtractor_1 (.a(x), .b(y), .out(out_4), .bin(in_1));  // open: bout

  // Notes on the sheet:
  //   Mateus Augusto Moraes Ferreira   Matricula:  435669
endmodule
