// Logisim project Exemplo0043.circ as structural Verilog: 1 circuit, main circuit main
module main (
  input  [5:0] x,
  input  [5:0] y,
  output out_3
);

  Comparator #(.width(6), .mode("unsigned")) comparator_1 (.a(x), .b(y), .eq(out_3));  // open: gt, lt

  // Notes on the sheet:
  //   Mateus Augusto Moraes Ferreira      Matricula: 435669
endmodule
