// Logisim project Exemplo0044.circ as structural Verilog: 1 circuit, main circuit main
module main (
  input  [5:0] x,
  input  [5:0] y,
  output out_3,
  output out_4
);

  Comparator #(.width(6), .mode("unsigned")) comparator_1 (.a(x), .b(y), .gt(out_3), .lt(out_4));  // open: eq

  // Notes on the sheet:
  //   Mateus Augusto Moraes Ferreira     Matricula: 435669
endmodule
