// Logisim project Exemplo0045.circ as structural Verilog: 1 circuit, main circuit main
module main (
  input  in_1,
  input  [5:0] x,
  input  [5:0] y,
  output [5:0] out_4,
  output out_5
);

  wire [5:0] not_1_out, not_2_out;

  assign not_1_out = ~x;  // NOT_Gate not_1, 6 bits wide
  assign not_2_out = ~y;  // NOT_Gate not_2, 6 bits wide
  Adder #(.width(6)) adder_1 (.a(not_1_out), .b(not_2_out), .out(out_4), .cin(in_1), .cout(out_5));

  // Notes on the sheet:
  //   Mateus Augusto Moraes Ferreira    Matricula: 435669
endmodule
