// Logisim project circuitos2.circ as structural Verilog: 10 circuits, main circuit MeiaSoma
module MeiaSoma (
  input  a,
  input  b,
  output carry,
  output s0
);

  and and_1 (carry, a, b);
  xor xor_1 (s0, a, b);
endmodule

module Ex01 (
  input  B0,
  input  A0,
  input  B1,
  input  A1,
  input  B2,
  input  A2,
  input  B3,
  input  A3,
  input  B4,
  input  A4,
  input  B5,
  input  A5,
  output s0,
  output s1,
  output s2,
  output s3,
  output s4,
  output s5,
  output carry
);

  wire meiasoma_1_carry, somadorcompleto_1_carry, somadorcompleto_2_carry, somadorcompleto_3_carry,
       somadorcompleto_4_carry;

  MeiaSoma meiasoma_1 (.a(A0), .b(B0), .carry(meiasoma_1_carry), .s0(s0));
  SomadorCompleto somadorcompleto_1 (
    .a(A1), .b(B1), .carry_in(meiasoma_1_carry), .carry(somadorcompleto_1_carry), .s0(s1));
  SomadorCompleto somadorcompleto_2 (
    .a(A2), .b(B2), .carry_in(somadorcompleto_1_carry), .carry(somadorcompleto_2_carry), .s0(s2));
  SomadorCompleto somadorcompleto_3 (
    .a(A3), .b(B3), .carry_in(somadorcompleto_2_carry), .carry(somadorcompleto_3_carry), .s0(s3));
  SomadorCompleto somadorcompleto_4 (
    .a(A4), .b(B4), .carry_in(somadorcompleto_3_carry), .carry(somadorcompleto_4_carry), .s0(s4));
  SomadorCompleto somadorcompleto_5 (.a(A5), .b(B5), .carry_in(somadorcompleto_4_carry), .carry(carry), .s0(s5));

  // Notes on the sheet:
  //   Somador 6 bits
endmodule

module SomadorCompleto (
  input  a,
  input  b,
  input  carry_in,
  output carry,
  output s0
);

  wire meiasoma_1_carry, meiasoma_1_s0, meiasoma_2_carry;

  MeiaSoma meiasoma_1 (.a(a), .b(b), .carry(meiasoma_1_carry), .s0(meiasoma_1_s0));
  MeiaSoma meiasoma_2 (.a(carry_in), .b(meiasoma_1_s0), .carry(meiasoma_2_carry), .s0(s0));
  or or_1 (carry, meiasoma_1_carry, meiasoma_2_carry);
endmodule

module Ex02 (
  input  B0,
  input  A0,
  input  B1,
  input  A1,
  input  B2,
  input  A2,
  input  B3,
  input  A3,
  input  B4,
  input  A4,
  input  B5,
  input  A5,
  output s0,
  output s1,
  output s2,
  output s3,
  output s4,
  output s5,
  output carry
);

  wire not_1_out, not_2_out, not_3_out, not_4_out, not_5_out, not_6_out, somadorcompleto_1_carry,
       somadorcompleto_2_carry, somadorcompleto_3_carry, somadorcompleto_4_carry, somadorcompleto_5_carry;

  not not_1 (not_1_out, B0);
  SomadorCompleto somadorcompleto_1 (.a(A0), .b(not_1_out), .carry_in(1'b1), .carry(somadorcompleto_1_carry), .s0(s0));
  not not_2 (not_2_out, B1);
  SomadorCompleto somadorcompleto_2 (
    .a(A1), .b(not_2_out), .carry_in(somadorcompleto_1_carry), .carry(somadorcompleto_2_carry), .s0(s1));
  not not_3 (not_3_out, B2);
  SomadorCompleto somadorcompleto_3 (
    .a(A2), .b(not_3_out), .carry_in(somadorcompleto_2_carry), .carry(somadorcompleto_3_carry), .s0(s2));
  not not_4 (not_4_out, B3);
  not not_5 (not_5_out, B4);
  SomadorCompleto somadorcompleto_4 (
    .a(A3), .b(not_4_out), .carry_in(somadorcompleto_3_carry), .carry(somadorcompleto_4_carry), .s0(s3));
  SomadorCompleto somadorcompleto_5 (
    .a(A4), .b(not_5_out), .carry_in(somadorcompleto_4_carry), .carry(somadorcompleto_5_carry), .s0(s4));
  not not_6 (not_6_out, B5);
  SomadorCompleto somadorcompleto_6 (.a(A5), .b(not_6_out), .carry_in(somadorcompleto_5_carry), .carry(carry), .s0(s5));

  // Notes on the sheet:
  //   Subtrator de 6 bits
endmodule

module Subtrator (
  input  a,
  input  b,
  input  carry_in,
  output carry,
  output s0
);

  wire meiasoma_1_carry, meiasoma_1_s0, meiasoma_2_carry, not_1_out;

  not not_1 (not_1_out, b);
  MeiaSoma meiasoma_1 (.a(a), .b(not_1_out), .carry(meiasoma_1_carry), .s0(meiasoma_1_s0));
  MeiaSoma meiasoma_2 (.a(carry_in), .b(meiasoma_1_s0), .carry(meiasoma_2_carry), .s0(s0));
  or or_1 (carry, meiasoma_1_carry, meiasoma_2_carry);
endmodule

module Igualdade (
  input  in_1,
  input  in_2,
  output out_3
);

  xnor xnor_1 (out_3, in_2, in_1);
endmodule

module Ex03 (
  input  A0,
  input  A1,
  input  A2,
  input  A3,
  input  A4,
  input  A5,
  input  B0,
  input  B1,
  input  B2,
  input  B3,
  input  B4,
  input  B5,
  output _1___Iguais__0_Diferentes
);

  wire igualdade_1_out_3, igualdade_2_out_3, igualdade_3_out_3, igualdade_4_out_3, igualdade_5_out_3,
       igualdade_6_out_3;

  Igualdade igualdade_1 (.in_1(A0), .in_2(B0), .out_3(igualdade_1_out_3));
  Igualdade igualdade_2 (.in_1(A1), .in_2(B1), .out_3(igualdade_2_out_3));
  Igualdade igualdade_3 (.in_1(A2), .in_2(B2), .out_3(igualdade_3_out_3));
  Igualdade igualdade_4 (.in_1(A3), .in_2(B3), .out_3(igualdade_4_out_3));
  and and_1 (_1___Iguais__0_Diferentes, igualdade_1_out_3, igualdade_2_out_3, igualdade_3_out_3, igualdade_4_out_3, igualdade_5_out_3, igualdade_6_out_3);
  Igualdade igualdade_5 (.in_1(A4), .in_2(B4), .out_3(igualdade_5_out_3));
  Igualdade igualdade_6 (.in_1(A5), .in_2(B5), .out_3(igualdade_6_out_3));

  // Notes on the sheet:
  //   Comparador para Igualdade
endmodule

module Ex04 (
  input  A0,
  input  A1,
  input  A2,
  input  A3,
  input  A4,
  input  A5,
  input  B0,
  input  B1,
  input  B2,
  input  B3,
  input  B4,
  input  B5,
  output _1___Diferente__0___Iguais
);

  wire ex03_1__1___iguais__0_diferentes;

  Ex03 ex03_1 (
    ._1___Iguais__0_Diferentes(ex03_1__1___iguais__0_diferentes), .A0(A0), .A1(A1), .A2(A2), .A3(A3),
    .A4(A4), .A5(A5), .B0(B0), .B1(B1), .B2(B2), .B3(B3), .B4(B4), .B5(B5));
  not not_1 (_1___Diferente__0___Iguais, ex03_1__1___iguais__0_diferentes);

  // Notes on the sheet:
  //   Comparador para Diferença
endmodule

module Comp_de1 (
  input  entrada,
  output Complemento_de_1
);

  not not_1 (Complemento_de_1, entrada);

  // Notes on the sheet:
  //   Complemento de 1
endmodule

module Ex05 (
  input  in_1,
  input  in_2,
  input  in_3,
  input  in_4,
  input  in_5,
  input  in_6,
  output out_7,
  output out_8,
  output out_9,
  output out_10,
  output out_11,
  output out_12,
  output out_13
);

  wire comp_de1_1_complemento_de_1, comp_de1_2_complemento_de_1, comp_de1_3_complemento_de_1,
       comp_de1_4_complemento_de_1, comp_de1_5_complemento_de_1, comp_de1_6_complemento_de_1,
       meiasoma_1_carry, not_1_out, not_2_out, not_3_out, not_4_out, not_5_out, somadorcompleto_2_carry,
       somadorcompleto_3_carry, somadorcompleto_4_carry, somadorcompleto_5_carry;

  Comp_de1 comp_de1_1 (.entrada(in_1), .Complemento_de_1(comp_de1_1_complemento_de_1));
  not not_1 (not_1_out, 1'b1);
  SomadorCompleto somadorcompleto_1 (
    .a(comp_de1_1_complemento_de_1), .b(not_1_out), .carry_in(somadorcompleto_3_carry), .carry(out_13),
    .s0(out_12));
  Comp_de1 comp_de1_2 (.entrada(in_2), .Complemento_de_1(comp_de1_2_complemento_de_1));
  Comp_de1 comp_de1_3 (.entrada(in_3), .Complemento_de_1(comp_de1_3_complemento_de_1));
  not not_2 (not_2_out, 1'b1);
  not not_3 (not_3_out, 1'b1);
  SomadorCompleto somadorcompleto_2 (
    .a(comp_de1_3_complemento_de_1), .b(not_3_out), .carry_in(somadorcompleto_5_carry),
    .carry(somadorcompleto_2_carry), .s0(out_10));
  SomadorCompleto somadorcompleto_3 (
    .a(comp_de1_2_complemento_de_1), .b(not_2_out), .carry_in(somadorcompleto_2_carry),
    .carry(somadorcompleto_3_carry), .s0(out_11));
  Comp_de1 comp_de1_4 (.entrada(in_4), .Complemento_de_1(comp_de1_4_complemento_de_1));
  Comp_de1 comp_de1_5 (.entrada(in_5), .Complemento_de_1(comp_de1_5_complemento_de_1));
  not not_4 (not_4_out, 1'b1);
  not not_5 (not_5_out, 1'b1);
  SomadorCompleto somadorcompleto_4 (
    .a(comp_de1_5_complemento_de_1), .b(not_4_out), .carry_in(meiasoma_1_carry),
    .carry(somadorcompleto_4_carry), .s0(out_8));
  SomadorCompleto somadorcompleto_5 (
    .a(comp_de1_4_complemento_de_1), .b(not_5_out), .carry_in(somadorcompleto_4_carry),
    .carry(somadorcompleto_5_carry), .s0(out_9));
  Comp_de1 comp_de1_6 (.entrada(in_6), .Complemento_de_1(comp_de1_6_complemento_de_1));
  MeiaSoma meiasoma_1 (.a(comp_de1_6_complemento_de_1), .b(1'b1), .carry(meiasoma_1_carry), .s0(out_7));

  // Notes on the sheet:
  //   Complemento de 2
endmodule
