// Logisim project Exemplo0021.circ as structural Verilog: 1 circuit, main circuit main
module main (
  input  [4:0] x,
  input  [4:0] y,
  output out_3,
  output [4:0] S,
  output [4:0] s2
);

  wire [4:0] and_1_out, and_2_out, or_1_out, or_2_out, undriven, xor_1_out;

  assign or_1_out = y | x;  // OR_Gate or_1, 5 bits wide
  assign and_1_out = x & y;  // AND_Gate and_1, 5 bits wide
  assign xor_1_out = undriven ^ or_1_out;  // XOR_Gate xor_1, 5 bits wide
  assign and_2_out = or_1_out & undriven;  // AND_Gate and_2, 5 bits wide
  assign or_2_out = and_2_out | and_1_out;  // OR_Gate or_2, 5 bits wide
endmodule
