// Logisim project Exemplo0022.circ as structural Verilog: 1 circuit, main circuit main
// Vai Um
module main (
  input  [5:0] x,
  input  [5:0] y,
  output [5:0] S0,
  output [5:0] S1
);

  wire [5:0] or_1_out, undriven, xor_1_out;

  assign x = ~x;  // NOT_Gate not_1, 6 bits wide
  assign xor_1_out = x ^ y;  // XOR_Gate xor_1, 6 bits wide
  // AND_Gate and_1 has open pins: in0=y, in2=x, out=open
  assign xor_1_out = ~xor_1_out;  // NOT_Gate not_2, 6 bits wide
  assign or_1_out = undriven | xor_1_out;  // OR_Gate or_1, 6 bits wide
  assign S1 = undriven & xor_1_out;  // AND_Gate and_2, 6 bits wide
endmodule
