// Logisim project Exemplo0023.circ as structural Verilog: 1 circuit, main circuit main
module main (
  input  [5:0] x,
  input  [5:0] y,
  output out_3
);

  Comparator #(.width(6)) comparator_1 (.a(x), .b(y), .eq(out_3));  // open: gt, lt
endmodule
