// Logisim project Ex 2.circ as structural Verilog: 2 circuits, main circuit main
module main (
  input  in_1,
  input  [4:0] in_2,
  input  [4:0] in_3,
  output [4:0] out_4,
  output out_5
);

  Sub sub_1 (.A(in_2), .B(in_3), .carryIn(in_1), .Saida(out_4), .carryout(out_5));
endmodule

module Sub (
  input  [4:0] A,
  input  [4:0] B,
  input  carryIn,
  output [4:0] Saida,
  output carryout
);

  wire and_1_out, and_2_out, and_3_out, and_4_out, and_5_out, and_6_out, and_7_out, and_8_out, and_9_out,
       and_10_out, not_1_out, not_2_out, not_3_out, not_4_out, not_5_out, not_6_out, not_7_out, not_8_out,
       not_9_out, not_10_out, or_1_out, or_2_out, or_3_out, or_4_out, xor_1_out, xor_2_out, xor_3_out,
       xor_4_out, xor_5_out;

  not not_1 (not_1_out, A[0]);
  not not_2 (not_2_out, A[1]);
  not not_3 (not_3_out, A[2]);
  not not_4 (not_4_out, A[3]);
  not not_5 (not_5_out, A[4]);
  xor xor_1 (xor_1_out, B[0], A[0]);
  not not_6 (not_6_out, xor_1_out);
  and and_1 (and_1_out, B[0], not_1_out);
  xor xor_2 (xor_2_out, B[1], A[1]);
  not not_7 (not_7_out, xor_2_out);
  and and_2 (and_2_out, B[1], not_2_out);
  xor xor_3 (xor_3_out, B[2], A[2]);
  not not_8 (not_8_out, xor_3_out);
  and and_3 (and_3_out, B[2], not_3_out);
  xor xor_4 (xor_4_out, B[3], A[3]);
  not not_9 (not_9_out, xor_4_out);
  and and_4 (and_4_out, B[3], not_4_out);
  xor xor_5 (xor_5_out, B[4], A[4]);
  not not_10 (not_10_out, xor_5_out);
  and and_5 (and_5_out, B[4], not_5_out);
  xor xor_6 (Saida[0], carryIn, xor_1_out);
  and and_6 (and_6_out, not_6_out, carryIn);
  xor xor_7 (Saida[1], or_1_out, xor_2_out);
  and and_7 (and_7_out, not_7_out, or_1_out);
  xor xor_8 (Saida[2], or_2_out, xor_3_out);
  and and_8 (and_8_out, not_8_out, or_2_out);
  xor xor_9 (Saida[3], or_3_out, xor_4_out);
  and and_9 (and_9_out, not_9_out, or_3_out);
  xor xor_10 (Saida[4], or_4_out, xor_5_out);
  and and_10 (and_10_out, not_10_out, or_4_out);
  // Probe on Saida[0]
  // Probe on or_1_out
  or or_1 (or_1_out, and_6_out, and_1_out);
  // Probe on Saida[1]
  or or_2 (or_2_out, and_7_out, and_2_out);
  // Probe on or_2_out
  // Probe on Saida[2]
  or or_3 (or_3_out, and_8_out, and_3_out);
  // Probe on or_3_out
  // Probe on Saida[3]
  // Probe on or_4_out
  or or_4 (or_4_out, and_9_out, and_4_out);
  // Probe on Saida[4]
  or or_5 (carryout, and_10_out, and_5_out);
  // Probe on carryout
endmodule
