// Logisim project Ex 3.circ as structural Verilog: 2 circuits, main circuit main
module main (
  input  [5:0] in_1,
  input  [5:0] in_2,
  output [5:0] out_3
);

  Compare compare_1 (.in_1(in_1), .in_2(in_2), .out_3(out_3));
endmodule

module Compare (
  input  [5:0] in_1,
  input  [5:0] in_2,
  output [5:0] out_3
);

  and and_1 (out_3[0], in_1[0], in_2[0]);
  and and_2 (out_3[1], in_1[1], in_2[1]);
  and and_3 (out_3[2], in_1[2], in_2[2]);
  and and_4 (out_3[3], in_1[3], in_2[3]);
  and and_5 (out_3[4], in_1[4], in_2[4]);
  and and_6 (out_3[5], in_2[5], in_1[5]);
endmodule
