// Logisim project Ex 4.circ as structural Verilog: 2 circuits, main circuit main
module main (
  input  [5:0] in_1,
  input  [5:0] in_2,
  output [5:0] out_3
);

  Compare compare_1 (.in_1(in_1), .in_2(in_2), .out_3(out_3));
endmodule

module Compare (
  input  [5:0] in_1,
  input  [5:0] in_2,
  output [5:0] out_3
);

  xor xor_1 (out_3[0], in_1[0], in_2[0]);
  xor xor_2 (out_3[1], in_1[1], in_2[1]);
  xor xor_3 (out_3[2], in_1[2], in_2[2]);
  xor xor_4 (out_3[3], in_1[3], in_2[3]);
  xor xor_5 (out_3[4], in_1[4], in_2[4]);
  xor xor_6 (out_3[5], in_2[5], in_1[5]);
endmodule
