// Logisim project Ex 5.circ as structural Verilog: 2 circuits, main circuit main
module main (
  input  [4:0] in_1,
  output [4:0] out_2,
  output out_3
);

  wire [4:0] not_1_out;

  assign not_1_out = ~in_1;  // NOT_Gate not_1, 5 bits wide
  Soma soma_1 (.A(not_1_out), .carryIn(1'b1), .Saida(out_2), .carryout(out_3));
endmodule

module Soma (
  input  [4:0] A,
  input  carryIn,
  output [4:0] Saida,
  output carryout
);

  wire and_1_out, and_2_out, and_3_out, and_4_out, and_5_out;

  xor xor_1 (Saida[0], carryIn, A[0]);
  and and_1 (and_1_out, A[0], carryIn);
  xor xor_2 (Saida[1], and_1_out, A[1]);
  and and_2 (and_2_out, A[1], and_1_out);
  xor xor_3 (Saida[2], and_2_out, A[2]);
  and and_3 (and_3_out, A[2], and_2_out);
  xor xor_4 (Saida[3], and_3_out, A[3]);
  and and_4 (and_4_out, A[3], and_3_out);
  xor xor_5 (Saida[4], and_4_out, A[4]);
  and and_5 (and_5_out, A[4], and_4_out);
  // Probe on Saida[0]
  // Probe on and_1_out
  // Probe on Saida[1]
  // Probe on and_2_out
  // Probe on Saida[2]
  // Probe on and_3_out
  // Probe on Saida[3]
  // Probe on and_4_out
  // Probe on Saida[4]
  // Probe on and_5_out
  not not_1 (carryout, and_5_out);
endmodule
