// Logisim project Exemplo0021.circ as structural Verilog: 1 circuit, main circuit main
module main (
  input  in_1,
  input  [5:0] in_2,
  input  [5:0] in_3,
  output [5:0] out_4,
  output out_5
);

  Adder #(.width(6)) adder_1 (.a(in_2), .b(in_3), .out(out_4), .cin(in_1), .cout(out_5));
endmodule
