// Logisim project Exercicio02.circ as structural Verilog: 1 circuit, main circuit main
module main (
  input  [5:0] carryIn,
  input  [5:0] a,
  input  [5:0] b,
  output [5:0] s,
  output [5:0] carryOut
);

  wire [5:0] and_1_out, and_2_out, and_3_out, not_1_out, xor_1_out;

  assign not_1_out = ~a;  // NOT_Gate not_1, 6 bits wide
  assign xor_1_out = a ^ b;  // XOR_Gate xor_1, 6 bits wide
  assign and_1_out = b & not_1_out;  // AND_Gate and_1, 6 bits wide
  assign and_2_out = not_1_out & carryIn;  // AND_Gate and_2, 6 bits wide
  assign and_3_out = b & carryIn;  // AND_Gate and_3, 6 bits wide
  assign s = carryIn ^ xor_1_out;  // XOR_Gate xor_2, 6 bits wide
  assign carryOut = and_1_out | and_2_out | and_3_out;  // OR_Gate or_1, 6 bits wide
endmodule
