// Logisim project Exercicio04.circ as structural Verilog: 1 circuit, main circuit main
module main (
  input  a1,
  input  b1,
  input  a2,
  input  b2,
  input  a3,
  input  b3,
  input  a4,
  input  b4,
  input  a5,
  input  b5,
  input  a6,
  input  b6,
  output Resultado
);

  wire xnor_1_out, xnor_2_out, xnor_3_out, xnor_4_out, xnor_5_out, xnor_6_out;

  xnor xnor_1 (xnor_1_out, a1, b1);
  xnor xnor_2 (xnor_2_out, a2, b2);
  xnor xnor_3 (xnor_3_out, a3, b3);
  xnor xnor_4 (xnor_4_out, a4, b4);
  xnor xnor_5 (xnor_5_out, a5, b5);
  xnor xnor_6 (xnor_6_out, a6, b6);
  nand nand_1 (Resultado, xnor_1_out, xnor_2_out, xnor_3_out, xnor_4_out, xnor_5_out, xnor_6_out);
endmodule
