// Logisim project Exercicio05.circ as structural Verilog: 1 circuit, main circuit main
module main (
  input  in_1,
  input  in_2,
  input  in_3,
  input  in_4,
  input  in_5,
  input  in_6,
  input  in_7,
  output out_8,
  output out_9,
  output out_10,
  output out_11,
  output out_12,
  output out_13
);

  wire not_1_out, not_2_out, not_3_out, not_4_out, not_5_out, not_6_out;

  not not_1 (not_1_out, in_2);
  not not_2 (not_2_out, in_3);
  not not_3 (not_3_out, in_4);
  not not_4 (not_4_out, in_5);
  not not_5 (not_5_out, in_6);
  not not_6 (not_6_out, in_7);
  xor xor_1 (out_8, in_1, not_1_out);
  xor xor_2 (out_9, in_1, not_2_out);
  xor xor_3 (out_10, in_1, not_3_out);
  xor xor_4 (out_11, in_1, not_4_out);
  xor xor_5 (out_12, in_1, not_5_out);
  xor xor_6 (out_13, in_1, not_6_out);
endmodule
