// Logisim project Exemplo0045.circ as structural Verilog: 2 circuits, main circuit main
module main (
  input  [5:0] a,
  input  C1,
  input  C2,
  output _0,
  output _1,
  output _2,
  output _3,
  output _4,
  output _5,
  output CarryOut
);

  wire c2_1_carryout, c2_2_carryout, c2_3_carryout, c2_4_carryout, c2_5_carryout;
  wire [5:0] not_1_out;

  assign not_1_out = ~a;  // NOT_Gate not_1, 6 bits wide
  C2 c2_1 (.CarryIn(C2), .A(not_1_out[5]), .B(C1), .S(_0), .CarryOut(c2_1_carryout));
  C2 c2_2 (.CarryIn(c2_1_carryout), .A(not_1_out[4]), .B(C1), .S(_1), .CarryOut(c2_2_carryout));
  C2 c2_3 (.CarryIn(c2_2_carryout), .A(not_1_out[3]), .B(C1), .S(_2), .CarryOut(c2_3_carryout));
  C2 c2_4 (.CarryIn(c2_3_carryout), .A(not_1_out[2]), .B(C1), .S(_3), .CarryOut(c2_4_carryout));
  C2 c2_5 (.CarryIn(c2_4_carryout), .A(not_1_out[1]), .B(C1), .S(_4), .CarryOut(c2_5_carryout));
  C2 c2_6 (.CarryIn(c2_5_carryout), .A(not_1_out[0]), .B(C1), .S(_5), .CarryOut(CarryOut));
endmodule

module C2 (
  input  CarryIn,
  input  A,
  input  B,
  output S,
  output CarryOut
);

  wire and1_out, and2_out, xor1_out;

  and and1 (and1_out, B, A);
  xor xor1 (xor1_out, A, B);
  and and2 (and2_out, CarryIn, xor1_out);
  xor xor2 (S, CarryIn, xor1_out);
  or or1 (CarryOut, and2_out, and1_out);
endmodule
