// Logisim project Exemplo0045.circ as structural Verilog: 2 circuits, main circuit main
module main (
  input  Carry_In,
  input  x,
  input  y,
  output S,
  output Carry_Out
);

  wire AND2_out, AND_1_out, XOR1_out;

  xor XOR1 (XOR1_out, x, y);
  and AND_1 (AND_1_out, y, x);
  and AND2 (AND2_out, Carry_In, XOR1_out);
  xor XOR2 (S, Carry_In, XOR1_out);
  or OR1 (Carry_Out, AND2_out, AND_1_out);

  // Notes on the sheet:
  //   w1
  //   w2
  //   w3
endmodule

module somadorcompleto (
  input  y,
  input  Carry_In,
  input  [5:0] x,
  output s0,
  output s1,
  output s2,
  output s3,
  output s4,
  output s5,
  output Carry_Out
);

  wire main_1_carry_out, main_2_carry_out, main_3_carry_out, main_4_carry_out, main_5_carry_out;
  wire [5:0] NOT1_out;

  assign NOT1_out = ~x;  // NOT_Gate NOT1, 6 bits wide
  main main_1 (.Carry_In(Carry_In), .x(NOT1_out[0]), .y(y), .S(s0), .Carry_Out(main_1_carry_out));
  main main_2 (.Carry_In(main_1_carry_out), .x(NOT1_out[1]), .y(y), .S(s1), .Carry_Out(main_2_carry_out));
  main main_3 (.Carry_In(main_2_carry_out), .x(NOT1_out[2]), .y(y), .S(s2), .Carry_Out(main_3_carry_out));
  main main_4 (.Carry_In(main_3_carry_out), .x(NOT1_out[3]), .y(y), .S(s3), .Carry_Out(main_4_carry_out));
  main main_5 (.Carry_In(main_4_carry_out), .x(NOT1_out[4]), .y(y), .S(s4), .Carry_Out(main_5_carry_out));
  main main_6 (.Carry_In(main_5_carry_out), .x(NOT1_out[5]), .y(y), .S(s5), .Carry_Out(Carry_Out));

  // Notes on the sheet:
  //   Mateus Augusto Moraes Ferreira   Matricula: 435669
  //   w1
  //   w2
  //   w3
  //   w4
  //   w5
endmodule
