// Logisim project Exemplo0041.circ as structural Verilog: 1 circuit, main circuit main
module main (
  input  [5:0] Carry_In,
  input  [5:0] x,
  input  [5:0] y,
  output [5:0] S,
  output [5:0] Carry_Out
);

  wire [5:0] AND2_out, AND_1_out, XOR1_out;

  assign XOR1_out = x ^ y;  // XOR_Gate XOR1, 6 bits wide
  assign AND_1_out = y & x;  // AND_Gate AND_1, 6 bits wide
  assign AND2_out = Carry_In & XOR1_out;  // AND_Gate AND2, 6 bits wide
  assign S = Carry_In ^ XOR1_out;  // XOR_Gate XOR2, 6 bits wide
  assign Carry_Out = AND2_out | AND_1_out;  // OR_Gate OR1, 6 bits wide

  // Notes on the sheet:
  //   w1
  //   w2
  //   Mateus Augusto Moraes Ferreira    Matricula:435669
  //   w3
endmodule
