// Logisim project Exemplo0042.circ as structural Verilog: 1 circuit, main circuit main
module main (
  input  [5:0] Borrow_In,
  input  [5:0] x,
  input  [5:0] y,
  output [5:0] S,
  output [5:0] Borrow_Out
);

  wire [5:0] AND2_out, AND_1_out, NOT1_out, NOT2_out, XOR1_out;

  assign NOT1_out = ~x;  // NOT_Gate NOT1, 6 bits wide
  assign XOR1_out = x ^ y;  // XOR_Gate XOR1, 6 bits wide
  assign AND_1_out = y & NOT1_out;  // AND_Gate AND_1, 6 bits wide
  assign NOT2_out = ~XOR1_out;  // NOT_Gate NOT2, 6 bits wide
  assign AND2_out = Borrow_In & NOT2_out;  // AND_Gate AND2, 6 bits wide
  assign S = Borrow_In ^ XOR1_out;  // XOR_Gate XOR2, 6 bits wide
  assign Borrow_Out = AND2_out | AND_1_out;  // OR_Gate OR1, 6 bits wide

  // Notes on the sheet:
  //   w1
  //   w2
  //   Mateus Augusto Moraes Ferreira    Matricula:435669
  //   w3
endmodule
