// Logisim project Exemplo0044.circ as structural Verilog: 1 circuit, main circuit main
module main (
  input  [5:0] x,
  input  [5:0] y,
  output out_3
);

  wire [5:0] xnor_1_out;

  assign xnor_1_out = ~(x ^ y);  // XNOR_Gate xnor_1, 6 bits wide
  nand nand_1 (out_3, xnor_1_out[0], xnor_1_out[1], xnor_1_out[2], xnor_1_out[3], xnor_1_out[4], xnor_1_out[5]);

  // Notes on the sheet:
  //   Mateus Augusto Moraes Ferreira    Matricula:435669
  //   0 - Equals   1 - Different
endmodule
