// Logisim project complementoseadders.circ as structural Verilog: 4 circuits, main circuit Half Adder
module Half_Adder (
  input  A,
  input  B,
  output S0,
  output S1
);

  xor xor_1 (S0, A, B);
  and and_1 (S1, A, B);
endmodule

module Full_Adder (
  input  A,
  input  B,
  input  V,
  output S0,
  output S1
);

  wire half_adder_1_s0, half_adder_1_s1, half_adder_2_s1;

  Half_Adder half_adder_1 (.A(A), .B(B), .S0(half_adder_1_s0), .S1(half_adder_1_s1));
  Half_Adder half_adder_2 (.A(half_adder_1_s0), .B(V), .S0(S0), .S1(half_adder_2_s1));
  or or_1 (S1, half_adder_2_s1, half_adder_1_s1);
endmodule

module ByteCompl2 (
  input  I7,
  input  I6,
  input  I5,
  input  I4,
  input  I3,
  input  I2,
  input  I1,
  input  I0,
  output OVERFLOW,
  output O7,
  output O6,
  output O5,
  output O4,
  output O3,
  output O2,
  output O1,
  output O0
);

  wire half_adder_1_s1, half_adder_2_s1, half_adder_3_s1, half_adder_4_s1, half_adder_5_s1, half_adder_6_s1,
       half_adder_7_s1, not_1_out, not_2_out, not_3_out, not_4_out, not_5_out, not_6_out, not_7_out,
       not_8_out;

  not not_1 (not_1_out, I7);
  not not_2 (not_2_out, I6);
  not not_3 (not_3_out, I5);
  not not_4 (not_4_out, I4);
  not not_5 (not_5_out, I3);
  not not_6 (not_6_out, I2);
  not not_7 (not_7_out, I1);
  not not_8 (not_8_out, I0);
  Half_Adder half_adder_1 (.A(not_8_out), .B(1'b1), .S0(O0), .S1(half_adder_1_s1));
  Half_Adder half_adder_2 (.A(not_6_out), .B(half_adder_3_s1), .S0(O2), .S1(half_adder_2_s1));
  Half_Adder half_adder_3 (.A(not_7_out), .B(half_adder_1_s1), .S0(O1), .S1(half_adder_3_s1));
  Half_Adder half_adder_4 (.A(not_5_out), .B(half_adder_2_s1), .S0(O3), .S1(half_adder_4_s1));
  Half_Adder half_adder_5 (.A(not_4_out), .B(half_adder_4_s1), .S0(O4), .S1(half_adder_5_s1));
  Half_Adder half_adder_6 (.A(not_3_out), .B(half_adder_5_s1), .S0(O5), .S1(half_adder_6_s1));
  Half_Adder half_adder_7 (.A(not_2_out), .B(half_adder_6_s1), .S0(O6), .S1(half_adder_7_s1));
  and and_1 (OVERFLOW, not_1_out, not_2_out, not_3_out, not_4_out, not_5_out, not_6_out, not_7_out, not_8_out);
  Half_Adder half_adder_8 (.A(not_1_out), .B(half_adder_7_s1), .S0(O7));  // open: S1
endmodule

module ByteCompl1 (
  input  I7,
  input  I6,
  input  I5,
  input  I4,
  input  I3,
  input  I2,
  input  I1,
  input  I0,
  output O7,
  output O6,
  output O5,
  output O4,
  output O3,
  output O2,
  output O1,
  output O0
);

  not not_1 (O7, I7);
  not not_2 (O6, I6);
  not not_3 (O5, I5);
  not not_4 (O4, I4);
  not not_5 (O3, I3);
  not not_6 (O2, I2);
  not not_7 (O1, I1);
  not not_8 (O0, I0);
endmodule
