// Logisim project Comparadores de 6 bits.circ as structural Verilog: 2 circuits, main circuit Comparador
// Comparador de igualdaade 6 bits
module Comparador (
  input  [5:0] in_1,
  input  [5:0] in_2,
  output [5:0] out_3
);

  xnor xnor_1 (out_3[0], in_2[0], in_1[0]);
  xnor xnor_2 (out_3[1], in_2[1], in_1[1]);
  xnor xnor_3 (out_3[2], in_2[2], in_1[2]);
  xnor xnor_4 (out_3[3], in_2[3], in_1[3]);
  xnor xnor_5 (out_3[4], in_2[4], in_1[4]);
  xnor xnor_6 (out_3[5], in_2[5], in_1[5]);
endmodule

module \Comparador_de_diferença  (
  input  [5:0] in_1,
  input  [5:0] in_2,
  output [5:0] out_3
);

  xor xor_1 (out_3[0], in_2[0], in_1[0]);
  xor xor_2 (out_3[1], in_2[1], in_1[1]);
  xor xor_3 (out_3[2], in_2[2], in_1[2]);
  xor xor_4 (out_3[3], in_2[3], in_1[3]);
  xor xor_5 (out_3[4], in_2[4], in_1[4]);
  xor xor_6 (out_3[5], in_2[5], in_1[5]);
endmodule
