// Logisim project Exemplo0021.circ as structural Verilog: 2 circuits, main circuit main
module main (
  input  in_1,
  input  in_2,
  input  in_3,
  input  in_4,
  input  in_5,
  input  in_6,
  input  in_7,
  input  in_8,
  input  in_9,
  input  in_10,
  input  in_11,
  output out_12,
  output out_13,
  output out_14,
  output out_15,
  output out_16,
  output out_17
);

  wire full_adder_1_c_out, full_adder_2_sum, full_adder_3_sum, full_adder_4_sum;

  full_adder full_adder_1 (.a(in_7), .b(in_4), .C_in(in_11), .Sum(out_17), .C_out(full_adder_1_c_out));
  full_adder full_adder_2 (.a(in_9), .b(in_10), .C_in(full_adder_1_c_out), .Sum(full_adder_2_sum), .C_out(out_16));
  full_adder full_adder_3 (.a(in_6), .b(in_8), .C_in(full_adder_2_sum), .Sum(full_adder_3_sum), .C_out(out_15));
  full_adder full_adder_4 (.a(in_2), .b(in_5), .C_in(full_adder_3_sum), .Sum(full_adder_4_sum), .C_out(out_14));
  full_adder full_adder_5 (.a(in_1), .b(in_3), .C_in(full_adder_4_sum), .Sum(out_12), .C_out(out_13));
endmodule

module full_adder (
  input  a,
  input  b,
  input  C_in,
  output Sum,
  output C_out
);

  wire and_1_out, and_2_out, xor_1_out, xor_2_out;

  xor xor_1 (xor_1_out, a, b);
  and and_1 (and_1_out, C_in, xor_2_out);
  xor xor_2 (xor_2_out, a, b);
  and and_2 (and_2_out, a, b);
  xor xor_3 (Sum, xor_1_out, C_in);
  or or_1 (C_out, and_1_out, and_2_out);
endmodule
