// Logisim project Exemplo0022.circ as structural Verilog: 2 circuits, main circuit main
module main (
  input  in_1,
  input  in_2,
  input  in_3,
  input  in_4,
  input  in_5,
  input  in_6,
  input  in_7,
  input  in_8,
  input  in_9,
  input  in_10,
  input  in_11,
  output out_12,
  output out_13,
  output out_14,
  output out_15,
  output out_16,
  output out_17
);

  wire full_subtractor_1_y, full_subtractor_2_y, full_subtractor_3_y, full_subtractor_4_y;

  full_subtractor full_subtractor_1 (.a(in_2), .b(in_6), .c(in_11), .x(out_14), .y(full_subtractor_1_y));
  full_subtractor full_subtractor_2 (.a(in_8), .b(in_3), .c(full_subtractor_1_y), .x(out_15), .y(full_subtractor_2_y));
  full_subtractor full_subtractor_3 (.a(in_9), .b(in_4), .c(full_subtractor_2_y), .x(out_16), .y(full_subtractor_3_y));
  full_subtractor full_subtractor_4 (.a(in_10), .b(in_5), .c(full_subtractor_3_y), .x(out_17), .y(full_subtractor_4_y));
  full_subtractor full_subtractor_5 (.a(in_7), .b(in_1), .c(full_subtractor_4_y), .x(out_13), .y(out_12));
endmodule

module full_subtractor (
  input  a,
  input  b,
  input  c,
  output x,
  output y
);

  wire and_1_out, and_2_out, and_3_out, and_4_out, and_5_out, and_6_out, and_7_out, not_1_out, not_2_out,
       not_3_out, not_4_out, not_5_out, not_6_out, not_7_out, not_8_out;

  not not_1 (not_1_out, a);
  not not_2 (not_2_out, b);
  not not_3 (not_3_out, a);
  not not_4 (not_4_out, c);
  not not_5 (not_5_out, b);
  not not_6 (not_6_out, c);
  not not_7 (not_7_out, b);
  not not_8 (not_8_out, b);
  and and_1 (and_1_out, not_1_out, not_2_out, c);
  and and_2 (and_2_out, not_3_out, b, not_4_out);
  and and_3 (and_3_out, a, not_5_out, not_6_out);
  and and_4 (and_4_out, a, b, c);
  and and_5 (and_5_out, not_7_out, c);
  and and_6 (and_6_out, a, not_8_out);
  and and_7 (and_7_out, a, c);
  or or_1 (x, and_1_out, and_2_out, and_3_out, and_4_out);
  or or_2 (y, and_5_out, and_6_out, and_7_out);
endmodule
