// Logisim project Exemplo0023.circ as structural Verilog: 2 circuits, main circuit main
module main (
  input  in_1,
  input  in_2,
  input  in_3,
  input  in_4,
  input  in_5,
  input  in_6,
  input  in_7,
  input  in_8,
  input  in_9,
  input  in_10,
  output out_11,
  output out_12,
  output out_13,
  output out_14,
  output out_15,
  output out_16
);

  comparator_equal comparator_equal_1 (.a(in_2), .b(in_1), .y(out_12));
  comparator_equal comparator_equal_2 (.a(in_4), .b(in_3), .y(out_13));
  comparator_equal comparator_equal_3 (.a(in_6), .b(in_5), .y(out_14));
  comparator_equal comparator_equal_4 (.a(in_8), .b(in_7), .y(out_15));
  comparator_equal comparator_equal_5 (.a(in_10), .b(in_9), .y(out_16));
  and and_1 (out_11, out_12, out_13, out_14, out_15, out_16);
endmodule

module comparator_equal (
  input  a,
  input  b,
  output y
);

  wire and_1_out, and_2_out, not_1_out, not_2_out;

  not not_1 (not_1_out, a);
  not not_2 (not_2_out, b);
  and and_1 (and_1_out, not_1_out, not_2_out);
  and and_2 (and_2_out, a, b);
  or or_1 (y, and_1_out, and_2_out);
endmodule
