// Logisim project Exemplo0024.circ as structural Verilog: 2 circuits, main circuit main
module main (
  input  in_1,
  input  in_2,
  input  in_3,
  input  in_4,
  input  in_5,
  input  in_6,
  input  in_7,
  input  in_8,
  input  in_9,
  input  in_10,
  output out_11,
  output out_12,
  output out_13,
  output out_14,
  output out_15,
  output out_16,
  output out_17,
  output out_18,
  output out_19,
  output out_20,
  output out_21
);

  wire or_1_out, or_2_out, or_3_out, or_4_out, or_5_out;

  comparator_dif comparator_dif_1 (.a(in_2), .b(in_1), .out_3(out_12), .out_4(out_11));
  or or_1 (or_1_out, out_11, out_12);
  comparator_dif comparator_dif_2 (.a(in_4), .b(in_3), .out_3(out_14), .out_4(out_13));
  or or_2 (or_2_out, out_13, out_14);
  comparator_dif comparator_dif_3 (.a(in_6), .b(in_5), .out_3(out_16), .out_4(out_15));
  or or_3 (or_3_out, out_15, out_16);
  and and_1 (out_21, or_1_out, or_2_out, or_4_out, or_3_out, or_5_out);
  comparator_dif comparator_dif_4 (.a(in_8), .b(in_7), .out_3(out_18), .out_4(out_17));
  or or_4 (or_4_out, out_17, out_18);
  comparator_dif comparator_dif_5 (.a(in_10), .b(in_9), .out_3(out_20), .out_4(out_19));
  or or_5 (or_5_out, out_19, out_20);
endmodule

module comparator_dif (
  input  a,
  input  b,
  output out_3,
  output out_4
);

  wire not_1_out, not_2_out;

  not not_1 (not_1_out, a);
  not not_2 (not_2_out, b);
  and and_1 (out_3, not_1_out, b);
  and and_2 (out_4, a, not_2_out);
endmodule
