// Logisim project Exemplo0025.circ as structural Verilog: 2 circuits, main circuit main
module main (
  input  in_1,
  input  in_2,
  input  in_3,
  input  in_4,
  input  in_5,
  output out_6,
  output out_7,
  output out_8,
  output out_9,
  output out_10,
  output out_11
);

  C_1 c_1_1 (.in_1(in_2), .out_2(out_7));
  C_1 c_1_2 (.in_1(in_3), .out_2(out_8));
  C_1 c_1_3 (.in_1(in_4), .out_2(out_10));
  C_1 c_1_4 (.in_1(in_5), .out_2(out_11));
  not not_1 (out_6, in_1);
  or or_1 (out_9, out_6, out_7, out_8, out_10, out_11);
endmodule

module C_1 (
  input  in_1,
  output out_2
);

  not nor_1 (out_2, in_1);  // NOR_Gate
endmodule
