// Logisim project Exemplo0021.circ as structural Verilog: 1 circuit, main circuit main
module main (
  input  Carry_In,
  input  [5:0] a,
  input  [5:0] b,
  input  [5:0] Carry_In_2,
  input  [5:0] a_2,
  input  [5:0] b_2,
  output [5:0] S,
  output Carry_Out,
  output [5:0] s0,
  output [5:0] Carry_Out_2
);

  wire [5:0] and1_out, and2_out, xor1_out;

  assign xor1_out = a_2 ^ b_2;  // XOR_Gate xor1, 6 bits wide
  assign and1_out = b_2 & a_2;  // AND_Gate and1, 6 bits wide
  Adder #(.width(6)) adder_1 (.a(a), .b(b), .out(S), .cin(Carry_In), .cout(Carry_Out));
  assign s0 = Carry_In_2 ^ xor1_out;  // XOR_Gate xor2, 6 bits wide
  assign and2_out = xor1_out & Carry_In_2;  // AND_Gate and2, 6 bits wide
  assign Carry_Out_2 = and2_out | and1_out;  // OR_Gate or1, 6 bits wide

  // Notes on the sheet:
  //   Ederson Cristiano Nunes - 438964
  //   s1
  //   s2
  //   s3
endmodule
