// Logisim project Exemplo0023.circ as structural Verilog: 1 circuit, main circuit main
module main (
  input  Carry_In,
  input  [5:0] a,
  input  [5:0] b,
  input  [5:0] borrow_In,
  input  [5:0] a_2,
  input  [5:0] b_2,
  output [5:0] S,
  output Carry_Out,
  output [5:0] s0,
  output [5:0] borrow_Out
);

  wire [5:0] and1_out, and2_out, not1_out, not2_out, xor1_out;

  assign not1_out = ~a_2;  // NOT_Gate not1, 6 bits wide
  assign xor1_out = a_2 ^ b_2;  // XOR_Gate xor1, 6 bits wide
  Subtractor #(.width(6)) subtractor_1 (.a(a), .b(b), .out(S), .bin(Carry_In), .bout(Carry_Out));
  assign not2_out = ~xor1_out;  // NOT_Gate not2, 6 bits wide
  assign s0 = borrow_In ^ xor1_out;  // XOR_Gate xor2, 6 bits wide
  assign and1_out = b_2 & not1_out;  // AND_Gate and1, 6 bits wide
  assign and2_out = borrow_In & not2_out;  // AND_Gate and2, 6 bits wide
  assign borrow_Out = and2_out | and1_out;  // OR_Gate or1, 6 bits wide

  // Notes on the sheet:
  //   Ederson Cristiano Nunes - 438964
  //   subtracao completa
  //   s1
  //   s2
  //   s3
endmodule
