// Logisim project Exemplo0024.circ as structural Verilog: 1 circuit, main circuit main
module main (
  input  [5:0] a,
  input  [5:0] b,
  output s0
);

  wire [5:0] xnor_1_out;

  assign xnor_1_out = ~(a ^ b);  // XNOR_Gate xnor_1, 6 bits wide
  nand nand_1 (s0, xnor_1_out[0], xnor_1_out[1], xnor_1_out[2], xnor_1_out[3], xnor_1_out[4], xnor_1_out[5]);

  // Notes on the sheet:
  //   Ederson Cristiano Nunes - 438964
  //   comparador para igualdade
  //   0  => igual   -    1 => diferente
  //   w1
endmodule
