// Logisim project Exercicio01.circ as structural Verilog: 1 circuit, main circuit main
module main (
  input  a,
  input  b,
  input  cIn,
  input  sinal_carry,
  output s,
  output cOut
);

  wire and_1_out, and_2_out, or_1_out, xor_1_out, xor_2_out;

  xor xor_1 (xor_1_out, a, b);
  and and_1 (and_1_out, b, cIn);
  xor xor_2 (xor_2_out, sinal_carry, a);
  or or_1 (or_1_out, b, cIn);
  and and_2 (and_2_out, xor_2_out, or_1_out);
  xor xor_3 (s, xor_1_out, cIn);
  or or_2 (cOut, and_1_out, and_2_out);
endmodule
