// Logisim project Exercicio05.circ as structural Verilog: 1 circuit, main circuit main
module main (
  input  a1,
  input  b1,
  input  a2,
  input  b2,
  input  a3,
  input  b3,
  input  a4,
  input  b4,
  input  a5,
  input  b5,
  input  a6,
  input  b6,
  output out_13,
  output out_14,
  output out_15,
  output out_16,
  output Resultado,
  output out_18,
  output out_19
);

  wire xnor_1_out, xnor_2_out, xnor_3_out, xnor_4_out, xnor_5_out, xnor_6_out;

  xor xor_1 (out_13, a1, b1);
  xor xor_2 (out_14, a2, b2);
  xor xor_3 (out_15, a3, b3);
  xor xor_4 (out_16, a4, b4);
  xor xor_5 (out_18, a5, b5);
  xor xor_6 (out_19, a6, b6);
  xnor xnor_1 (xnor_1_out, a1, b1);
  xnor xnor_2 (xnor_2_out, a2, b2);
  xnor xnor_3 (xnor_3_out, a3, b3);
  xnor xnor_4 (xnor_4_out, a4, b4);
  xnor xnor_5 (xnor_5_out, a5, b5);
  xnor xnor_6 (xnor_6_out, a6, b6);
  nand nand_1 (Resultado, xnor_1_out, xnor_2_out, xnor_3_out, xnor_4_out, xnor_5_out, xnor_6_out);
endmodule
