// Logisim project Ex 2.circ as structural Verilog: 3 circuits, main circuit main
module main (
  input  in_1,
  input  [4:0] in_2,
  input  [4:0] in_3,
  output out_4,
  output [4:0] out_5,
  output out_6
);

  wire soma_1_carryout;
  wire [4:0] bit_extender_1_out, xor_1_out;

  assign bit_extender_1_out = {{4{in_1}}, in_1};  // Bit_Extender bit_extender_1
  assign xor_1_out = in_3 ^ bit_extender_1_out;  // XOR_Gate xor_1, 5 bits wide
  Soma soma_1 (.A(in_2), .B(xor_1_out), .carryIn(in_1), .Saida(out_5), .carryout(soma_1_carryout));
  xor xor_2 (out_6, soma_1_carryout, in_1);
  igual_a_0 igual_a_0_1 (.in_1(out_5), .out_2(out_4));
endmodule

module Soma (
  input  [4:0] A,
  input  [4:0] B,
  input  carryIn,
  output [4:0] Saida,
  output carryout
);

  wire and_1_out, and_2_out, and_3_out, and_4_out, and_5_out, and_6_out, and_7_out, and_8_out, and_9_out,
       and_10_out, or_1_out, or_2_out, or_3_out, or_4_out, xor_1_out, xor_2_out, xor_3_out, xor_4_out,
       xor_5_out;

  xor xor_1 (xor_1_out, B[0], A[0]);
  and and_1 (and_1_out, B[0], A[0]);
  xor xor_2 (xor_2_out, B[1], A[1]);
  and and_2 (and_2_out, B[1], A[1]);
  xor xor_3 (xor_3_out, B[2], A[2]);
  and and_3 (and_3_out, B[2], A[2]);
  xor xor_4 (xor_4_out, B[3], A[3]);
  and and_4 (and_4_out, B[3], A[3]);
  xor xor_5 (xor_5_out, B[4], A[4]);
  and and_5 (and_5_out, B[4], A[4]);
  xor xor_6 (Saida[0], carryIn, xor_1_out);
  and and_6 (and_6_out, xor_1_out, carryIn);
  xor xor_7 (Saida[1], or_1_out, xor_2_out);
  and and_7 (and_7_out, xor_2_out, or_1_out);
  xor xor_8 (Saida[2], or_2_out, xor_3_out);
  and and_8 (and_8_out, xor_3_out, or_2_out);
  xor xor_9 (Saida[3], or_3_out, xor_4_out);
  and and_9 (and_9_out, xor_4_out, or_3_out);
  xor xor_10 (Saida[4], or_4_out, xor_5_out);
  and and_10 (and_10_out, xor_5_out, or_4_out);
  // Probe on Saida[0]
  // Probe on or_1_out
  or or_1 (or_1_out, and_6_out, and_1_out);
  // Probe on Saida[1]
  or or_2 (or_2_out, and_7_out, and_2_out);
  // Probe on or_2_out
  // Probe on Saida[2]
  or or_3 (or_3_out, and_8_out, and_3_out);
  // Probe on or_3_out
  // Probe on Saida[3]
  // Probe on or_4_out
  or or_4 (or_4_out, and_9_out, and_4_out);
  // Probe on Saida[4]
  // Probe on carryout
  or or_5 (carryout, and_10_out, and_5_out);
endmodule

module igual_a_0 (
  input  [4:0] in_1,
  output out_2
);

  wire or_1_out;

  or or_1 (or_1_out, in_1[0], in_1[1], in_1[2], in_1[3], in_1[4]);
  not not_1 (out_2, or_1_out);
endmodule
