// Logisim project Ex 5.circ as structural Verilog: 2 circuits, main circuit main
module main (
  input  [5:0] in_1,
  input  [5:0] in_2
);
endmodule

module Maior (
  input  [5:0] in_1,
  input  [5:0] in_2,
  output [5:0] out_3
);

  wire and_1_out, and_2_out, and_3_out, and_4_out, and_5_out, and_6_out, not_1_out, not_2_out, not_3_out,
       not_4_out, not_5_out, not_6_out;

  and and_1 (and_1_out, in_1[0], not_1_out);
  not not_1 (not_1_out, in_2[0]);
  and and_2 (and_2_out, in_1[1], not_2_out);
  not not_2 (not_2_out, in_2[1]);
  and and_3 (and_3_out, in_1[2], not_3_out);
  not not_3 (not_3_out, in_2[2]);
  and and_4 (and_4_out, in_1[3], not_4_out);
  not not_4 (not_4_out, in_2[3]);
  and and_5 (and_5_out, in_1[4], not_5_out);
  not not_5 (not_5_out, in_2[4]);
  not not_6 (not_6_out, in_1[5]);
  and and_6 (and_6_out, not_6_out, in_2[5]);
endmodule
