// Logisim project Exemplo 1.circ as structural Verilog: 3 circuits, main circuit main
module main (
  input  in_1,
  input  [5:0] A,
  input  [5:0] B,
  output [5:0] out_4,
  output out_5
);

  wire adder_1_cout, not_1_out, or_1_out, subtractor_1_bout, xor_4_out;
  wire [5:0] clock_6bits_1_out_1, clock_6bits_1_out_2, copiadora_1_out_2, subtractor_1_out, xor_1_out,
       xor_3_out;

  Clock_6bits clock_6bits_1 (.out_1(clock_6bits_1_out_1), .out_2(clock_6bits_1_out_2));
  // Probe on clock_6bits_1_out_1
  // Probe on clock_6bits_1_out_2
  Copiadora copiadora_1 (.in_1(in_1), .out_2(copiadora_1_out_2));
  assign xor_1_out = clock_6bits_1_out_2 ^ copiadora_1_out_2;  // XOR_Gate xor_1, 6 bits wide
  Adder #(.width(6)) adder_1 (.a(clock_6bits_1_out_1), .b(xor_1_out), .out(out_4), .cin(in_1), .cout(adder_1_cout));
  not not_1 (not_1_out, in_1);
  Subtractor #(.width(6)) subtractor_1 (
    .a(clock_6bits_1_out_1), .b(clock_6bits_1_out_2), .out(subtractor_1_out), .bin(not_1_out),
    .bout(subtractor_1_bout));
  // Probe on subtractor_1_out
  xor xor_2 (out_5, adder_1_cout, in_1);
  // Probe on xor_3_out
  assign xor_3_out = subtractor_1_out ^ out_4;  // XOR_Gate xor_3, 6 bits wide
  xor xor_4 (xor_4_out, subtractor_1_bout, out_5);
  or or_1 (or_1_out, xor_3_out[0], xor_3_out[1], xor_3_out[2], xor_3_out[3], xor_3_out[4], xor_3_out[5]);
  // Probe on or_1_out
  // Probe on xor_4_out
endmodule

module Copiadora (
  input  in_1,
  output [5:0] out_2
);

  assign out_2 = {{5{in_1}}, in_1};  // Bit_Extender bit_extender_1
endmodule

module Clock_6bits (
  output [5:0] out_1,
  output [5:0] out_2
);

  Clock clock_1 (.out(out_1[0]));
  Clock #(.highDuration(2)) clock_2 (.out(out_1[1]));
  Clock #(.highDuration(4)) clock_3 (.out(out_1[2]));
  Clock #(.highDuration(8)) clock_4 (.out(out_1[3]));
  Clock #(.highDuration(16)) clock_5 (.out(out_1[4]));
  Clock #(.highDuration(32)) clock_6 (.out(out_1[5]));
  Clock #(.lowDuration(32)) clock_7 (.out(out_2[0]));
  Clock #(.highDuration(2), .lowDuration(32)) clock_8 (.out(out_2[1]));
  Clock #(.highDuration(4), .lowDuration(32)) clock_9 (.out(out_2[2]));
  Clock #(.highDuration(8), .lowDuration(32)) clock_10 (.out(out_2[3]));
  Clock #(.highDuration(16), .lowDuration(32)) clock_11 (.out(out_2[4]));
  Clock #(.highDuration(32), .lowDuration(32)) clock_12 (.out(out_2[5]));
endmodule
