// Logisim project Comparador.circ as structural Verilog: 4 circuits, main circuit Maior que
// >
module Maior_que (
  input  in_1,
  input  in_2,
  output out_3
);

  wire not_1_out;

  not not_1 (not_1_out, in_2);
  and and_1 (out_3, in_1, not_1_out);
endmodule

// <
module Menor_que (
  input  in_1,
  input  in_2,
  output out_3
);

  wire not_1_out;

  not not_1 (not_1_out, in_1);
  and and_1 (out_3, not_1_out, in_2);
endmodule

// =
module Igual (
  input  in_1,
  input  in_2,
  output out_3
);

  xnor xnor_1 (out_3, in_1, in_2);
endmodule

module ComparadoI (
  input  [4:0] in_1,
  input  [4:0] in_2,
  output out_3,
  output out_4,
  output out_5
);

  wire and_1_out, and_2_out, and_3_out, and_5_out, and_6_out, and_7_out, and_8_out, and_9_out, and_10_out,
       igual_1_out_3, igual_2_out_3, igual_3_out_3, igual_4_out_3, igual_5_out_3, maior_que_1_out_3,
       maior_que_2_out_3, maior_que_3_out_3, maior_que_4_out_3, maior_que_5_out_3, not_1_out, not_2_out,
       not_3_out, xor_1_out;

  Maior_que maior_que_1 (.in_1(in_1[0]), .in_2(in_2[0]), .out_3(maior_que_1_out_3));
  Maior_que maior_que_2 (.in_1(in_1[1]), .in_2(in_2[1]), .out_3(maior_que_2_out_3));
  Maior_que maior_que_3 (.in_1(in_1[2]), .in_2(in_2[2]), .out_3(maior_que_3_out_3));
  Maior_que maior_que_4 (.in_1(in_1[3]), .in_2(in_2[3]), .out_3(maior_que_4_out_3));
  not not_1 (not_1_out, maior_que_5_out_3);
  Maior_que maior_que_5 (.in_1(in_1[4]), .in_2(in_2[4]), .out_3(maior_que_5_out_3));
  Menor_que menor_que_1 (.in_1(in_1[0]), .in_2(in_2[0]));  // open: out_3
  Menor_que menor_que_2 (.in_1(in_1[1]), .in_2(in_2[1]));  // open: out_3
  Menor_que menor_que_3 (.in_1(in_1[2]), .in_2(in_2[2]));  // open: out_3
  Menor_que menor_que_4 (.in_1(in_1[3]), .in_2(in_2[3]));  // open: out_3
  Menor_que menor_que_5 (.in_1(in_1[4]), .in_2(in_2[4]));  // open: out_3
  Igual igual_1 (.in_1(in_1[0]), .in_2(in_2[0]), .out_3(igual_1_out_3));
  Igual igual_2 (.in_1(in_1[1]), .in_2(in_2[1]), .out_3(igual_2_out_3));
  Igual igual_3 (.in_1(in_1[2]), .in_2(in_2[2]), .out_3(igual_3_out_3));
  Igual igual_4 (.in_1(in_1[3]), .in_2(in_2[3]), .out_3(igual_4_out_3));
  Igual igual_5 (.in_1(in_1[4]), .in_2(in_2[4]), .out_3(igual_5_out_3));
  and and_1 (and_1_out, igual_2_out_3, igual_3_out_3);
  and and_2 (and_2_out, igual_4_out_3, igual_5_out_3);
  and and_3 (and_3_out, maior_que_4_out_3, igual_5_out_3);
  xor xor_1 (xor_1_out, not_1_out, igual_5_out_3);
  and and_4 (out_5, igual_1_out_3, igual_2_out_3, igual_3_out_3, igual_4_out_3, igual_5_out_3);
  and and_5 (and_5_out, and_1_out, and_2_out);
  and and_6 (and_6_out, igual_3_out_3, and_2_out);
  and and_7 (and_7_out, maior_que_3_out_3, and_2_out);
  and and_8 (and_8_out, maior_que_1_out_3, and_5_out);
  and and_9 (and_9_out, maior_que_2_out_3, and_6_out);
  and and_10 (and_10_out, maior_que_1_out_3, and_8_out);
  or or_1 (out_3, xor_1_out, and_10_out, and_9_out, and_7_out, and_3_out);
  not not_2 (not_2_out, out_3);
  not not_3 (not_3_out, out_5);
  and and_11 (out_4, not_2_out, not_3_out);
endmodule
