// Logisim project SomadorAlgebrico.circ as structural Verilog: 8 circuits, main circuit Somador Algébrico
module \Somador_Algébrico  (
  input  in_1,
  input  [4:0] A,
  input  [4:0] B,
  output [4:0] out_4,
  output out_5
);

  wire adder_1_cout;
  wire [4:0] bit_extender_1_out, xor_1_out;

  assign bit_extender_1_out = {{4{in_1}}, in_1};  // Bit_Extender bit_extender_1
  assign xor_1_out = B ^ bit_extender_1_out;  // XOR_Gate xor_1, 5 bits wide
  Adder #(.width(5)) adder_1 (.a(A), .b(xor_1_out), .out(out_4), .cin(in_1), .cout(adder_1_cout));
  xor xor_2 (out_5, adder_1_cout, in_1);
endmodule

module soma_completa (
  input  a,
  input  b___c,
  input  c,
  output out_4,
  output out_5
);

  wire meia_soma_1_out_4, meia_soma_2_out_3, meia_soma_2_out_4;

  meia_soma meia_soma_1 (.in_1(a), .in_2(meia_soma_2_out_3), .out_3(out_4), .out_4(meia_soma_1_out_4));
  meia_soma meia_soma_2 (.in_1(b___c), .in_2(c), .out_3(meia_soma_2_out_3), .out_4(meia_soma_2_out_4));
  or or_1 (out_5, meia_soma_1_out_4, meia_soma_2_out_4);
endmodule

module meia_soma (
  input  in_1,
  input  in_2,
  output out_3,
  output out_4
);

  xor xor_1 (out_3, in_1, in_2);
  and and_1 (out_4, in_1, in_2);
endmodule

module somador (
  input  [4:0] in_1,
  input  [4:0] in_2,
  input  in_3,
  output [4:0] out_4,
  output out_5
);

  wire soma_completa_2_out_5, soma_completa_3_out_5, soma_completa_4_out_5, soma_completa_5_out_5;

  soma_completa soma_completa_1 (
    .a(soma_completa_2_out_5), .b___c(in_1[4]), .c(in_2[4]), .out_4(out_4[4]), .out_5(out_5));
  soma_completa soma_completa_2 (
    .a(soma_completa_3_out_5), .b___c(in_1[3]), .c(in_2[3]), .out_4(out_4[3]), .out_5(soma_completa_2_out_5));
  soma_completa soma_completa_3 (
    .a(soma_completa_4_out_5), .b___c(in_1[2]), .c(in_2[2]), .out_4(out_4[2]), .out_5(soma_completa_3_out_5));
  soma_completa soma_completa_4 (
    .a(soma_completa_5_out_5), .b___c(in_1[1]), .c(in_2[1]), .out_4(out_4[1]), .out_5(soma_completa_4_out_5));
  soma_completa soma_completa_5 (
    .a(in_3), .b___c(in_1[0]), .c(in_2[0]), .out_4(out_4[0]), .out_5(soma_completa_5_out_5));
endmodule

module \Conferir_Resultado_da_Operaçao  (
  input  in_1,
  input  [4:0] A,
  input  [4:0] B,
  output out_4,
  output out_5
);

  wire adder_1_cout, igual_1_out_2, igual_2_out_2, igual_3_out_2, igual_4_out_2, igual_5_out_2;
  wire [4:0] adder_1_out, bit_extender_1_out, xor_1_out;

  assign bit_extender_1_out = {{4{in_1}}, in_1};  // Bit_Extender bit_extender_1
  assign xor_1_out = B ^ bit_extender_1_out;  // XOR_Gate xor_1, 5 bits wide
  Adder #(.width(5)) adder_1 (.a(A), .b(xor_1_out), .out(adder_1_out), .cin(in_1), .cout(adder_1_cout));
  xor xor_2 (out_5, adder_1_cout, in_1);
  Igual igual_1 (.in_1(adder_1_out[0]), .out_2(igual_1_out_2));
  Igual igual_2 (.in_1(adder_1_out[1]), .out_2(igual_2_out_2));
  Igual igual_3 (.in_1(adder_1_out[2]), .out_2(igual_3_out_2));
  Igual igual_4 (.in_1(adder_1_out[3]), .out_2(igual_4_out_2));
  Igual igual_5 (.in_1(adder_1_out[4]), .out_2(igual_5_out_2));
  and and_1 (out_4, igual_1_out_2, igual_2_out_2, igual_3_out_2, igual_4_out_2, igual_5_out_2);
endmodule

module Incremento_de_1 (
  input  [4:0] in_1,
  output out_2,
  output [4:0] out_3
);

  wire [4:0] bit_extender_1_out;

  assign bit_extender_1_out = {{4{1'b0}}, 1'b0};  // Bit_Extender bit_extender_1
  somador somador (.in_1(bit_extender_1_out), .in_2(in_1), .out_4(out_3), .in_3(1'b1), .out_5(out_2));
endmodule

module Decremento_de_1 (
  input  [4:0] in_1,
  output [4:0] out_2,
  output out_3
);

  wire adder_1_cout, xor_1_out;
  wire [4:0] bit_extender_1_out;

  xor xor_1 (xor_1_out, 1'b1, 1'b0);
  assign bit_extender_1_out = {{4{xor_1_out}}, xor_1_out};  // Bit_Extender bit_extender_1
  Adder #(.width(5)) adder_1 (.a(in_1), .b(bit_extender_1_out), .out(out_2), .cin(1'b0), .cout(adder_1_cout));
  xor xor_2 (out_3, adder_1_cout, 1'b0);
endmodule

// =
module Igual (
  input  in_1,
  output out_2
);

  nor nor_1 (out_2, in_1, 1'b0);
endmodule
