// Logisim project Exemplo0033.circ as structural Verilog: 4 circuits, main circuit main
module main (
  input  [5:0] x,
  input  [5:0] y,
  input  _0__soma____1__sub,
  output [5:0] Resultado,
  output Overflow,
  output _0_nao_1_sim
);

  wire or_1_out, or_2_out, or_3_out, or_4_out, or_5_out, or_6_out, sc_1_s1, somaparalelo_1_vai_um_2,
       somaparalelo_2_vai_um_2, somaparalelo_3_vai_um_2, somaparalelo_4_vai_um_2, somaparalelo_5_vai_um_2,
       xor_2_out, xor_3_out, xor_4_out, xor_5_out, xor_6_out, xor_7_out;

  xor xor_1 (Overflow, _0__soma____1__sub, sc_1_s1);
  xor xor_2 (xor_2_out, y[5], _0__soma____1__sub);
  SC sc_1 (.Vai_um(somaparalelo_1_vai_um_2), .y(x[5]), .x(xor_2_out), .s1(sc_1_s1), .s2(Resultado[5]));
  xor xor_3 (xor_3_out, _0__soma____1__sub, y[4]);
  xor xor_4 (xor_4_out, _0__soma____1__sub, y[3]);
  SomaParalelo somaparalelo_1 (
    .vai_um(somaparalelo_2_vai_um_2), .y(xor_3_out), .x(x[4]), .s0(Resultado[4]),
    .Vai_um_2(somaparalelo_1_vai_um_2));
  xor xor_5 (xor_5_out, _0__soma____1__sub, y[2]);
  SomaParalelo somaparalelo_2 (
    .vai_um(somaparalelo_3_vai_um_2), .y(xor_4_out), .x(x[3]), .s0(Resultado[3]),
    .Vai_um_2(somaparalelo_2_vai_um_2));
  SomaParalelo somaparalelo_3 (
    .vai_um(somaparalelo_4_vai_um_2), .y(xor_5_out), .x(x[2]), .s0(Resultado[2]),
    .Vai_um_2(somaparalelo_3_vai_um_2));
  or or_1 (or_1_out, Resultado[5], or_6_out);
  or or_2 (or_2_out, Overflow, or_1_out);
  xor xor_6 (xor_6_out, _0__soma____1__sub, y[0]);
  xor xor_7 (xor_7_out, _0__soma____1__sub, y[1]);
  SomaParalelo somaparalelo_4 (
    .vai_um(somaparalelo_5_vai_um_2), .y(xor_7_out), .x(x[1]), .s0(Resultado[1]),
    .Vai_um_2(somaparalelo_4_vai_um_2));
  or or_3 (or_3_out, Resultado[1], Resultado[0]);
  or or_4 (or_4_out, Resultado[2], or_3_out);
  or or_5 (or_5_out, Resultado[3], or_4_out);
  or or_6 (or_6_out, Resultado[4], or_5_out);
  SomaParalelo somaparalelo_5 (
    .vai_um(_0__soma____1__sub), .y(xor_6_out), .x(x[0]), .s0(Resultado[0]),
    .Vai_um_2(somaparalelo_5_vai_um_2));
  not not_1 (_0_nao_1_sim, or_2_out);

  // Notes on the sheet:
  //   -
endmodule

module MS (
  input  in_1,
  input  in_2,
  output out_3,
  output out_4
);

  xor xor_1 (out_3, in_1, in_2);
  and and_1 (out_4, in_2, in_1);
endmodule

module SC (
  input  Vai_um,
  input  y,
  input  x,
  output s1,
  output s2
);

  wire ms_1_out_3, ms_1_out_4, ms_3_out_4;

  MS ms_1 (.in_1(y), .in_2(x), .out_3(ms_1_out_3), .out_4(ms_1_out_4));
  MS ms_2 ();  // open: in_1, in_2, out_3, out_4
  MS ms_3 (.in_1(Vai_um), .in_2(ms_1_out_3), .out_3(s2), .out_4(ms_3_out_4));
  or or_1 (s1, ms_3_out_4, ms_1_out_4);
endmodule

module SomaParalelo (
  input  y,
  input  x,
  input  vai_um,
  output s0,
  output Vai_um_2
);

  SC sc_1 (.Vai_um(vai_um), .y(x), .x(y), .s1(Vai_um_2), .s2(s0));
endmodule
