// Logisim project Exemplo0034.circ as structural Verilog: 4 circuits, main circuit main
module main (
  input  [5:0] x,
  input  [5:0] y,
  input  Diminuir_1,
  input  _0__soma____1__sub,
  input  minus_1_para_sub,
  input  in_6,
  input  in_7,
  input  in_8,
  input  in_9,
  input  in_10,
  output Overflow,
  output Overflow_2,
  output [5:0] Resultado
);

  wire sc_1_s1, sc_1_s2, somaparalelo_1_vai_um_2, somaparalelo_2_s0, somaparalelo_2_vai_um_2,
       somaparalelo_3_vai_um_2, somaparalelo_4_s0, somaparalelo_4_vai_um_2, somaparalelo_5_s0,
       somaparalelo_5_vai_um_2, somaparalelo_6_vai_um_2, somaparalelo_7_vai_um_2, somaparalelo_8_s0,
       somaparalelo_8_vai_um_2, somaparalelo_9_vai_um_2, somaparalelo_10_s0, somaparalelo_10_vai_um_2,
       somaparalelo_11_vai_um_2, xor_3_out, xor_4_out, xor_5_out, xor_6_out, xor_7_out, xor_8_out, xor_9_out,
       xor_10_out, xor_11_out, xor_12_out, xor_13_out, xor_14_out;

  xor xor_1 (Overflow, _0__soma____1__sub, sc_1_s1);
  xor xor_2 (Overflow_2, minus_1_para_sub, somaparalelo_1_vai_um_2);
  xor xor_3 (xor_3_out, y[5], _0__soma____1__sub);
  SC sc_1 (.Vai_um(somaparalelo_2_vai_um_2), .y(x[5]), .x(xor_3_out), .s1(sc_1_s1), .s2(sc_1_s2));
  xor xor_4 (xor_4_out, minus_1_para_sub, in_6);
  SomaParalelo somaparalelo_1 (
    .vai_um(somaparalelo_3_vai_um_2), .y(xor_4_out), .x(sc_1_s2), .s0(Resultado[5]),
    .Vai_um_2(somaparalelo_1_vai_um_2));
  xor xor_5 (xor_5_out, _0__soma____1__sub, y[4]);
  xor xor_6 (xor_6_out, _0__soma____1__sub, y[3]);
  SomaParalelo somaparalelo_2 (
    .vai_um(somaparalelo_5_vai_um_2), .y(xor_5_out), .x(x[4]), .s0(somaparalelo_2_s0),
    .Vai_um_2(somaparalelo_2_vai_um_2));
  xor xor_7 (xor_7_out, minus_1_para_sub, in_8);
  xor xor_8 (xor_8_out, minus_1_para_sub, in_7);
  SomaParalelo somaparalelo_3 (
    .vai_um(somaparalelo_6_vai_um_2), .y(xor_8_out), .x(somaparalelo_2_s0), .s0(Resultado[4]),
    .Vai_um_2(somaparalelo_3_vai_um_2));
  xor xor_9 (xor_9_out, _0__soma____1__sub, y[2]);
  SomaParalelo somaparalelo_4 (
    .vai_um(somaparalelo_8_vai_um_2), .y(xor_9_out), .x(x[2]), .s0(somaparalelo_4_s0),
    .Vai_um_2(somaparalelo_4_vai_um_2));
  SomaParalelo somaparalelo_5 (
    .vai_um(somaparalelo_4_vai_um_2), .y(xor_6_out), .x(x[3]), .s0(somaparalelo_5_s0),
    .Vai_um_2(somaparalelo_5_vai_um_2));
  xor xor_10 (xor_10_out, minus_1_para_sub, in_9);
  SomaParalelo somaparalelo_6 (
    .vai_um(somaparalelo_7_vai_um_2), .y(xor_7_out), .x(somaparalelo_5_s0), .s0(Resultado[3]),
    .Vai_um_2(somaparalelo_6_vai_um_2));
  SomaParalelo somaparalelo_7 (
    .vai_um(somaparalelo_9_vai_um_2), .y(xor_10_out), .x(somaparalelo_4_s0), .s0(Resultado[2]),
    .Vai_um_2(somaparalelo_7_vai_um_2));
  xor xor_11 (xor_11_out, _0__soma____1__sub, y[0]);
  xor xor_12 (xor_12_out, _0__soma____1__sub, y[1]);
  SomaParalelo somaparalelo_8 (
    .vai_um(somaparalelo_10_vai_um_2), .y(xor_12_out), .x(x[1]), .s0(somaparalelo_8_s0),
    .Vai_um_2(somaparalelo_8_vai_um_2));
  xor xor_13 (xor_13_out, minus_1_para_sub, in_10);
  SomaParalelo somaparalelo_9 (
    .vai_um(somaparalelo_11_vai_um_2), .y(xor_13_out), .x(somaparalelo_8_s0), .s0(Resultado[1]),
    .Vai_um_2(somaparalelo_9_vai_um_2));
  SomaParalelo somaparalelo_10 (
    .vai_um(_0__soma____1__sub), .y(xor_11_out), .x(x[0]), .s0(somaparalelo_10_s0),
    .Vai_um_2(somaparalelo_10_vai_um_2));
  xor xor_14 (xor_14_out, minus_1_para_sub, Diminuir_1);
  SomaParalelo somaparalelo_11 (
    .vai_um(minus_1_para_sub), .y(xor_14_out), .x(somaparalelo_10_s0), .s0(Resultado[0]),
    .Vai_um_2(somaparalelo_11_vai_um_2));

  // Notes on the sheet:
  //   -
endmodule

module MS (
  input  in_1,
  input  in_2,
  output out_3,
  output out_4
);

  xor xor_1 (out_3, in_1, in_2);
  and and_1 (out_4, in_2, in_1);
endmodule

module SC (
  input  Vai_um,
  input  y,
  input  x,
  output s1,
  output s2
);

  wire ms_1_out_3, ms_1_out_4, ms_3_out_4;

  MS ms_1 (.in_1(y), .in_2(x), .out_3(ms_1_out_3), .out_4(ms_1_out_4));
  MS ms_2 ();  // open: in_1, in_2, out_3, out_4
  MS ms_3 (.in_1(Vai_um), .in_2(ms_1_out_3), .out_3(s2), .out_4(ms_3_out_4));
  or or_1 (s1, ms_3_out_4, ms_1_out_4);
endmodule

// SC
module SomaParalelo (
  input  y,
  input  x,
  input  vai_um,
  output s0,
  output Vai_um_2
);

  SC sc_1 (.Vai_um(vai_um), .y(x), .x(y), .s1(Vai_um_2), .s2(s0));
endmodule
