// Logisim project Exemplo0035.circ as structural Verilog: 4 circuits, main circuit main
module main (
  input  [5:0] x,
  input  [5:0] y,
  input  \_1___comparador_subtraçao_2___soma ,
  output _0___Maior_1_Menor,
  output _0__igual_1_diferente,
  output [5:0] Resultado
);

  wire or_1_out, or_2_out, or_3_out, or_4_out, sc_1_s1, somaparalelo_1_vai_um_2, somaparalelo_2_vai_um_2,
       somaparalelo_3_vai_um_2, somaparalelo_4_vai_um_2, somaparalelo_5_vai_um_2, xor_2_out, xor_3_out,
       xor_4_out, xor_5_out, xor_6_out, xor_7_out;

  xor xor_1 (_0___Maior_1_Menor, \_1___comparador_subtraçao_2___soma , sc_1_s1);
  xor xor_2 (xor_2_out, y[5], \_1___comparador_subtraçao_2___soma );
  SC sc_1 (.Vai_um(somaparalelo_1_vai_um_2), .y(x[5]), .x(xor_2_out), .s1(sc_1_s1), .s2(Resultado[5]));
  xor xor_3 (xor_3_out, \_1___comparador_subtraçao_2___soma , y[3]);
  xor xor_4 (xor_4_out, \_1___comparador_subtraçao_2___soma , y[4]);
  SomaParalelo somaparalelo_1 (
    .vai_um(somaparalelo_3_vai_um_2), .y(xor_4_out), .x(x[4]), .s0(Resultado[4]),
    .Vai_um_2(somaparalelo_1_vai_um_2));
  xor xor_5 (xor_5_out, \_1___comparador_subtraçao_2___soma , y[2]);
  SomaParalelo somaparalelo_2 (
    .vai_um(somaparalelo_4_vai_um_2), .y(xor_5_out), .x(x[2]), .s0(Resultado[2]),
    .Vai_um_2(somaparalelo_2_vai_um_2));
  SomaParalelo somaparalelo_3 (
    .vai_um(somaparalelo_2_vai_um_2), .y(xor_3_out), .x(x[3]), .s0(Resultado[3]),
    .Vai_um_2(somaparalelo_3_vai_um_2));
  xor xor_6 (xor_6_out, \_1___comparador_subtraçao_2___soma , y[0]);
  xor xor_7 (xor_7_out, \_1___comparador_subtraçao_2___soma , y[1]);
  SomaParalelo somaparalelo_4 (
    .vai_um(somaparalelo_5_vai_um_2), .y(xor_7_out), .x(x[1]), .s0(Resultado[1]),
    .Vai_um_2(somaparalelo_4_vai_um_2));
  or or_1 (or_1_out, Resultado[0], Resultado[2]);
  SomaParalelo somaparalelo_5 (
    .vai_um(\_1___comparador_subtraçao_2___soma ), .y(xor_6_out), .x(x[0]), .s0(Resultado[0]),
    .Vai_um_2(somaparalelo_5_vai_um_2));
  or or_2 (or_2_out, or_1_out, Resultado[1]);
  or or_3 (or_3_out, or_2_out, Resultado[3]);
  or or_4 (or_4_out, or_3_out, Resultado[4]);
  or or_5 (_0__igual_1_diferente, or_4_out, Resultado[5]);

  // Notes on the sheet:
  //   -
endmodule

module MS (
  input  in_1,
  input  in_2,
  output out_3,
  output out_4
);

  xor xor_1 (out_3, in_1, in_2);
  and and_1 (out_4, in_2, in_1);
endmodule

module SC (
  input  Vai_um,
  input  y,
  input  x,
  output s1,
  output s2
);

  wire ms_1_out_3, ms_1_out_4, ms_3_out_4;

  MS ms_1 (.in_1(y), .in_2(x), .out_3(ms_1_out_3), .out_4(ms_1_out_4));
  MS ms_2 ();  // open: in_1, in_2, out_3, out_4
  MS ms_3 (.in_1(Vai_um), .in_2(ms_1_out_3), .out_3(s2), .out_4(ms_3_out_4));
  or or_1 (s1, ms_3_out_4, ms_1_out_4);
endmodule

// SC
module SomaParalelo (
  input  y,
  input  x,
  input  vai_um,
  output s0,
  output Vai_um_2
);

  SC sc_1 (.Vai_um(vai_um), .y(x), .x(y), .s1(Vai_um_2), .s2(s0));
endmodule
