// Logisim project Guia05 - COnt.circ as structural Verilog
module Equal0 (
  input  in_1,
  input  in_2,
  input  in_3,
  input  in_4,
  input  in_5,
  input  in_6,
  output out_7
);

  wire or_1_out, or_2_out, or_3_out, or_4_out, or_5_out;

  or or_1 (or_1_out, in_1, in_2);
  or or_2 (or_2_out, in_3, in_4);
  or or_3 (or_3_out, in_5, in_6);
  or or_4 (or_4_out, or_1_out, or_2_out);
  not not_1 (out_7, or_5_out);
  or or_5 (or_5_out, or_4_out, or_3_out);
endmodule

module Incremento1 (
  input  in_1,
  input  in_2,
  input  in_3,
  input  in_4,
  input  in_5,
  input  in_6
);

  wire not_1_out, or_1_out;

  not not_1 (not_1_out, in_1);
  or or_1 (or_1_out, in_1, not_1_out);

  // Notes on the sheet:
  //   HalfAdder
endmodule

module Comparador (
  input  in_1,
  input  in_2,
  input  in_3,
  input  in_4,
  input  in_5,
  input  in_6,
  input  in_7,
  input  in_8,
  input  in_9,
  input  in_10,
  input  in_11,
  input  in_12,
  output A_B
);

  wire and_1_out, and_2_out, CG_2_out_3, CG_3_out_3, CG_out_3, compbitless_1_out_3, not_1_out, not_2_out;

  CompBitGreater CG (.in_1(in_1), .in_2(in_7), .out_3(CG_out_3));
  CompBitGreater CG_2 (.in_1(in_2), .in_2(in_8), .out_3(CG_2_out_3));
  CompBitGreater CG_3 (.in_1(in_3), .in_2(in_9), .out_3(CG_3_out_3));
  not not_1 (not_1_out, CG_out_3);
  not not_2 (not_2_out, CG_2_out_3);
  CompBitLess compbitless_1 (.in_1(in_1), .in_2(in_7), .out_3(compbitless_1_out_3));
  and and_1 (and_1_out, not_1_out, CG_2_out_3);
  and and_2 (and_2_out, not_2_out, CG_3_out_3);
  or or_1 (A_B, CG_out_3, and_1_out, and_2_out);
endmodule

module CompBitGreater (
  input  in_1,
  input  in_2,
  output out_3
);

  wire not_1_out;

  and and_1 (out_3, in_1, not_1_out);
  not not_1 (not_1_out, in_2);
endmodule

module CompBitLess (
  input  in_1,
  input  in_2,
  output out_3
);

  wire not_1_out;

  not not_1 (not_1_out, in_1);
  and and_1 (out_3, not_1_out, in_2);
endmodule

module CompEqual (
  input  in_1,
  input  in_2,
  output out_3
);

  wire and_1_out, and_2_out, not_1_out, not_2_out;

  and and_1 (and_1_out, in_1, in_2);
  not not_1 (not_1_out, in_1);
  and and_2 (and_2_out, not_1_out, not_2_out);
  not not_2 (not_2_out, in_2);
  or or_1 (out_3, and_1_out, and_2_out);
endmodule
