// Logisim project Exemplo0032.circ as structural Verilog: 1 circuit, main circuit main
module main (
  input  a,
  input  b,
  input  op,
  output s1,
  output s0,
  output _0,
  output _0_2
);

  wire adder_1_cout, xor_2_out;

  xor xor_1 (s1, op, adder_1_cout);
  xor xor_2 (xor_2_out, b, op);
  Adder #(.width(1)) adder_1 (.a(xor_2_out), .b(a), .out(s0), .cin(op), .cout(adder_1_cout));
  xor xor_3 (_0, s1, s0);
  xnor xnor_1 (_0_2, s1, s0);

  // Notes on the sheet:
  //   0 - soma
  //   1 - subtração
endmodule
