// Logisim project sumsub.circ as structural Verilog: 1 circuit, main circuit main
module main (
  input  a,
  input  b,
  input  op,
  output s1,
  output s0
);

  wire adder_1_cout, xor_2_out;

  xor xor_1 (s1, op, adder_1_cout);
  xor xor_2 (xor_2_out, b, op);
  Adder #(.width(1)) adder_1 (.a(xor_2_out), .b(a), .out(s0), .cin(op), .cout(adder_1_cout));

  // Notes on the sheet:
  //   0 - soma
  //   1 - subtração
endmodule
