// Logisim project guia5.circ as structural Verilog: 16 circuits, main circuit MeiaSoma
module MeiaSoma (
  input  a,
  input  b,
  output s1,
  output s0
);

  xor xor_1 (s1, a, b);
  and and_1 (s0, a, b);
endmodule

// FA
module FullAdder (
  input  carryIn,
  input  a,
  input  b,
  output s1,
  output s0
);

  wire meiasoma_1_s0, meiasoma_1_s1, meiasoma_2_s0;

  MeiaSoma meiasoma_1 (.a(a), .b(b), .s1(meiasoma_1_s1), .s0(meiasoma_1_s0));
  MeiaSoma meiasoma_2 (.a(carryIn), .b(meiasoma_1_s1), .s1(s0), .s0(meiasoma_2_s0));
  or or_1 (s1, meiasoma_2_s0, meiasoma_1_s0);
endmodule

// Subtrator
module Exemplo0031 (
  input  [5:0] in_1,
  input  [5:0] in_2,
  input  in_3,
  output out_4,
  output out_5,
  output out_6,
  output out_7,
  output out_8,
  output out_9,
  output OverFlow
);

  wire fafs_1_s1, fafs_2_s1, fafs_3_s1, fafs_4_s1, fafs_5_s1, fafs_6_s1;

  FAFS fafs_1 (.a(in_1[4]), .b(in_2[4]), .CarryIn(fafs_6_s1), .Sel(in_3), .s1(fafs_1_s1), .s0(out_5));
  FAFS fafs_2 (.a(in_1[5]), .b(in_2[5]), .CarryIn(fafs_1_s1), .Sel(in_3), .s1(fafs_2_s1), .s0(out_4));
  xor xor_1 (OverFlow, in_3, fafs_2_s1);
  FAFS fafs_3 (.a(in_1[0]), .b(in_2[0]), .CarryIn(in_3), .Sel(in_3), .s1(fafs_3_s1), .s0(out_9));
  FAFS fafs_4 (.a(in_1[1]), .b(in_2[1]), .CarryIn(fafs_3_s1), .Sel(in_3), .s1(fafs_4_s1), .s0(out_8));
  FAFS fafs_5 (.a(in_1[2]), .b(in_2[2]), .CarryIn(fafs_4_s1), .Sel(in_3), .s1(fafs_5_s1), .s0(out_7));
  FAFS fafs_6 (.a(in_1[3]), .b(in_2[3]), .CarryIn(fafs_5_s1), .Sel(in_3), .s1(fafs_6_s1), .s0(out_6));
endmodule

module FAFS (
  input  a,
  input  b,
  input  CarryIn,
  input  Sel,
  output s1,
  output s0
);

  wire xor_1_out;

  xor xor_1 (xor_1_out, b, Sel);
  FullAdder fulladder_1 (.a(a), .b(xor_1_out), .carryIn(CarryIn), .s1(s1), .s0(s0));
endmodule

module Exemplo0032 (
  input  [5:0] in_1,
  input  [5:0] in_2,
  input  in_3,
  output [5:0] out_4,
  output out_5
);

  Exemplo0031 exemplo0031_1 (
    .in_1(in_1), .in_2(in_2), .out_4(out_4[5]), .out_5(out_4[4]), .out_6(out_4[3]), .out_7(out_4[2]),
    .out_8(out_4[1]), .out_9(out_4[0]), .in_3(in_3));  // open: OverFlow
  F0 f0_1 (.in_1(out_4), .out_2(out_5));
endmodule

module F0 (
  input  [5:0] in_1,
  output out_2
);

  wire not_1_out, not_2_out, not_3_out, not_4_out, not_5_out, not_6_out;

  not not_1 (not_1_out, in_1[0]);
  not not_2 (not_2_out, in_1[2]);
  not not_3 (not_3_out, in_1[1]);
  not not_4 (not_4_out, in_1[5]);
  not not_5 (not_5_out, in_1[3]);
  not not_6 (not_6_out, in_1[4]);
  and and_1 (out_2, not_1_out, not_3_out, not_2_out, not_5_out, not_6_out, not_4_out);
endmodule

module Exemplo0033 (
  input  [5:0] in_1,
  input  [5:0] in_2,
  input  [5:0] in_3,
  input  in_4,
  output [5:0] out_5
);

  wire [5:0] m1_1_out_4;

  Exemplo0031 exemplo0031_1 (
    .in_1(in_1), .in_2(m1_1_out_4), .out_4(out_5[5]), .out_5(out_5[4]), .out_6(out_5[3]), .out_7(out_5[2]),
    .out_8(out_5[1]), .out_9(out_5[0]), .in_3(in_4));  // open: OverFlow
  M1 m1_1 (.in_1(in_2), .in_2(in_3), .out_4(m1_1_out_4), .in_3(in_4));
endmodule

module M1 (
  input  [5:0] in_1,
  input  [5:0] in_2,
  input  in_3,
  output [5:0] out_4
);

  Exemplo0031 exemplo0031_1 (
    .in_1(in_1), .in_2(in_2), .out_4(out_4[5]), .out_5(out_4[4]), .out_6(out_4[3]), .out_7(out_4[2]),
    .out_8(out_4[1]), .out_9(out_4[0]), .in_3(in_3));  // open: OverFlow
endmodule

module Exemplo0034 (
  input  [5:0] in_1,
  input  [5:0] in_2,
  input  [5:0] in_3,
  input  in_4,
  output [5:0] out_5
);

  wire [5:0] m1_1_out_4, me1_1_out_2;

  Exemplo0031 exemplo0031_1 (
    .in_1(in_2), .in_2(m1_1_out_4), .out_4(out_5[5]), .out_5(out_5[4]), .out_6(out_5[3]), .out_7(out_5[2]),
    .out_8(out_5[1]), .out_9(out_5[0]), .in_3(in_4));  // open: OverFlow
  Me1 me1_1 (.in_1(in_1), .out_2(me1_1_out_2));
  M1 m1_1 (.in_1(in_3), .in_2(me1_1_out_2), .out_4(m1_1_out_4), .in_3(in_4));
endmodule

module Me1 (
  input  [5:0] in_1,
  output [5:0] out_2
);

  wire fafs_1_s1, fafs_2_s1, fafs_3_s1, fafs_4_s1, fafs_5_s1, fafs_6_s1;

  FAFS fafs_1 (.a(in_1[4]), .b(in_1[4]), .CarryIn(fafs_6_s1), .Sel(1'b1), .s1(fafs_1_s1), .s0(out_2[4]));
  FAFS fafs_2 (.a(in_1[5]), .b(in_1[5]), .CarryIn(fafs_1_s1), .Sel(1'b1), .s1(fafs_2_s1), .s0(out_2[5]));
  FAFS fafs_3 (.a(in_1[0]), .b(in_1[0]), .CarryIn(1'b1), .Sel(1'b1), .s1(fafs_3_s1), .s0(out_2[0]));
  FAFS fafs_4 (.a(in_1[1]), .b(in_1[1]), .CarryIn(fafs_3_s1), .Sel(1'b1), .s1(fafs_4_s1), .s0(out_2[1]));
  FAFS fafs_5 (.a(in_1[2]), .b(in_1[2]), .CarryIn(fafs_4_s1), .Sel(1'b1), .s1(fafs_5_s1), .s0(out_2[2]));
  FAFS fafs_6 (.a(in_1[3]), .b(in_1[3]), .CarryIn(fafs_5_s1), .Sel(1'b1), .s1(fafs_6_s1), .s0(out_2[3]));
endmodule

// Subtrator
module Exemplo0035 (
  input  in_1,
  input  in_2,
  input  [5:0] in_3,
  input  [5:0] in_4,
  output out_5
);

  wire and_1_out, and_2_out, and_3_out, igual_1_out_3, maior_1_out_3, menor_1_out_3, not_1_out, not_2_out,
       not_3_out, not_4_out, or_1_out;

  igual igual_1 (.in_1(in_3), .in_2(in_4), .out_3(igual_1_out_3));
  maior maior_1 (.in_1(in_3), .in_2(in_4), .out_3(maior_1_out_3));
  menor menor_1 (.in_1(in_3), .in_2(in_4), .out_3(menor_1_out_3));
  not not_1 (not_1_out, in_1);
  not not_2 (not_2_out, in_1);
  not not_3 (not_3_out, in_2);
  not not_4 (not_4_out, in_2);
  and and_1 (and_1_out, igual_1_out_3, not_4_out, not_1_out);
  and and_2 (and_2_out, maior_1_out_3, in_2, not_2_out);
  and and_3 (and_3_out, menor_1_out_3, not_3_out, in_1);
  or or_1 (or_1_out, and_1_out, and_2_out);
  or or_2 (out_5, or_1_out, and_3_out);
endmodule

// =
module igual (
  input  [5:0] in_1,
  input  [5:0] in_2,
  output out_3
);

  wire and_1_out, and_2_out, and_3_out, and_4_out, xnor_1_out, xnor_2_out, xnor_3_out, xnor_4_out,
       xnor_5_out, xnor_6_out;

  xnor xnor_1 (xnor_1_out, in_1[5], in_2[5]);
  xnor xnor_2 (xnor_2_out, in_1[4], in_2[4]);
  xnor xnor_3 (xnor_3_out, in_1[3], in_2[3]);
  xnor xnor_4 (xnor_4_out, in_1[2], in_2[2]);
  xnor xnor_5 (xnor_5_out, in_1[1], in_2[1]);
  xnor xnor_6 (xnor_6_out, in_1[0], in_2[0]);
  and and_1 (and_1_out, xnor_1_out, xnor_2_out);
  and and_2 (and_2_out, xnor_3_out, xnor_4_out);
  and and_3 (and_3_out, xnor_5_out, xnor_6_out);
  and and_4 (and_4_out, and_1_out, and_2_out);
  and and_5 (out_3, and_4_out, and_3_out);
endmodule

// >
module maior (
  input  [5:0] in_1,
  input  [5:0] in_2,
  output out_3
);

  wire and_1_out, and_2_out, and_3_out, and_4_out, and_5_out, and_6_out, not_1_out, not_2_out, not_3_out,
       not_4_out, not_5_out, not_6_out, or_1_out, or_2_out, or_3_out, or_4_out;

  and and_1 (and_1_out, in_1[5], not_1_out);
  and and_2 (and_2_out, in_1[4], not_2_out);
  and and_3 (and_3_out, in_1[3], not_3_out);
  and and_4 (and_4_out, in_1[2], not_4_out);
  and and_5 (and_5_out, in_1[1], not_5_out);
  and and_6 (and_6_out, in_1[0], not_6_out);
  not not_1 (not_1_out, in_2[5]);
  not not_2 (not_2_out, in_2[4]);
  not not_3 (not_3_out, in_2[3]);
  not not_4 (not_4_out, in_2[2]);
  not not_5 (not_5_out, in_2[1]);
  not not_6 (not_6_out, in_2[0]);
  or or_1 (or_1_out, and_1_out, and_2_out);
  or or_2 (or_2_out, and_3_out, and_4_out);
  or or_3 (or_3_out, and_5_out, and_6_out);
  or or_4 (or_4_out, or_1_out, or_2_out);
  or or_5 (out_3, or_4_out, or_3_out);
endmodule

// <
module menor (
  input  [5:0] in_1,
  input  [5:0] in_2,
  output out_3
);

  wire and_1_out, and_2_out, and_3_out, and_4_out, and_5_out, and_6_out, not_1_out, not_2_out, not_3_out,
       not_4_out, not_5_out, not_6_out, or_1_out, or_2_out, or_3_out, or_4_out;

  not not_1 (not_1_out, in_1[5]);
  and and_1 (and_1_out, not_1_out, in_2[5]);
  not not_2 (not_2_out, in_1[4]);
  and and_2 (and_2_out, not_2_out, in_2[4]);
  not not_3 (not_3_out, in_1[3]);
  and and_3 (and_3_out, not_3_out, in_2[3]);
  not not_4 (not_4_out, in_1[2]);
  and and_4 (and_4_out, not_4_out, in_2[2]);
  not not_5 (not_5_out, in_1[1]);
  and and_5 (and_5_out, not_5_out, in_2[1]);
  not not_6 (not_6_out, in_1[0]);
  and and_6 (and_6_out, not_6_out, in_2[0]);
  or or_1 (or_1_out, and_1_out, and_2_out);
  or or_2 (or_2_out, and_3_out, and_4_out);
  or or_3 (or_3_out, and_5_out, and_6_out);
  or or_4 (or_4_out, or_1_out, or_2_out);
  or or_5 (out_3, or_4_out, or_3_out);
endmodule

module menorv2 (
  input  [5:0] in_1,
  input  [5:0] in_2,
  output out_3
);

  wire exemplo0031_1_out_4;

  Exemplo0031 exemplo0031_1 (
    .in_1(in_1), .in_2(in_2), .out_4(exemplo0031_1_out_4), .in_3(1'b1));  // open: OverFlow, out_5, out_6, out_7, out_8, out_9
  and and_1 (out_3, exemplo0031_1_out_4, 1'b1);
endmodule

module maiorv2 (
  input  [5:0] in_1,
  input  [5:0] in_2,
  output out_3
);

  wire and_1_out, exemplo0031_1_out_4, igual_1_out_3, not_1_out;

  Exemplo0031 exemplo0031_1 (
    .in_1(in_1), .in_2(in_2), .out_4(exemplo0031_1_out_4), .in_3(1'b1));  // open: OverFlow, out_5, out_6, out_7, out_8, out_9
  and and_1 (and_1_out, exemplo0031_1_out_4, 1'b1);
  not not_1 (not_1_out, and_1_out);
  xor xor_1 (out_3, not_1_out, igual_1_out_3);
  igual igual_1 (.in_1(in_1), .in_2(in_2), .out_3(igual_1_out_3));
endmodule
