// Logisim project Exemplo0034.circ as structural Verilog: 7 circuits, main circuit main
module main (
  input  in_1,
  input  in_2,
  input  in_3,
  input  in_4,
  input  in_5,
  input  in_6,
  input  in_7,
  input  in_8,
  input  in_9,
  input  in_10,
  input  in_11,
  input  in_12,
  input  in_13,
  output out_14,
  output out_15,
  output out_16,
  output out_17,
  output out_18,
  output out_19,
  output out_20
);

  wire and_1_out, and_2_out, and_3_out, and_4_out, and_5_out, and_6_out, and_7_out, and_8_out, and_9_out,
       and_10_out, and_11_out, and_12_out, comp2_1_out_7, comp2_1_out_8, comp2_1_out_9, comp2_1_out_10,
       comp2_1_out_11, comp2_1_out_12, DEC_out_7, DEC_out_8, DEC_out_9, DEC_out_10, DEC_out_11, DEC_out_12,
       fulladder_1_s, \fulladder_1_çarry , fulladder_2_s, \fulladder_2_çarry , fulladder_3_s,
       \fulladder_3_çarry , fulladder_4_s, \fulladder_4_çarry , fulladder_5_s, \fulladder_5_çarry ,
       fulladder_6_s, \fulladder_6_çarry , fulladder_7_s, \fulladder_7_çarry , fulladder_8_s, fulladder_9_s,
       \fulladder_9_çarry , fulladder_10_s, halfadder_1_carry, halfadder_1_s, halfadder_2_carry,
       halfadder_2_s, not_1_out;

  Dec1 DEC (
    .in_1(in_2), .in_2(in_3), .in_3(in_4), .in_4(in_5), .in_5(in_6), .in_6(in_7), .out_7(DEC_out_7),
    .out_8(DEC_out_8), .out_9(DEC_out_9), .out_10(DEC_out_10), .out_11(DEC_out_11), .out_12(DEC_out_12));
  Comp2 comp2_1 (
    .in_1(in_8), .in_2(in_9), .in_3(in_10), .in_4(in_11), .in_5(in_12), .in_6(in_13), .out_7(comp2_1_out_7),
    .out_8(comp2_1_out_8), .out_9(comp2_1_out_9), .out_10(comp2_1_out_10), .out_11(comp2_1_out_11),
    .out_12(comp2_1_out_12));
  HalfAdder halfadder_1 (.A(DEC_out_7), .B(in_8), .S(halfadder_1_s), .Carry(halfadder_1_carry));
  HalfAdder halfadder_2 (.A(DEC_out_7), .B(comp2_1_out_7), .S(halfadder_2_s), .Carry(halfadder_2_carry));
  FullAdder fulladder_1 (
    .A(DEC_out_8), .B(in_9), .Carry(halfadder_1_carry), .S(fulladder_1_s), .\Çarry (\fulladder_1_çarry ));
  FullAdder fulladder_2 (
    .A(DEC_out_9), .B(in_10), .Carry(\fulladder_1_çarry ), .S(fulladder_2_s), .\Çarry (\fulladder_2_çarry ));
  FullAdder fulladder_3 (
    .A(DEC_out_8), .B(comp2_1_out_8), .Carry(halfadder_2_carry), .S(fulladder_3_s),
    .\Çarry (\fulladder_3_çarry ));
  FullAdder fulladder_4 (
    .A(DEC_out_9), .B(comp2_1_out_9), .Carry(\fulladder_3_çarry ), .S(fulladder_4_s),
    .\Çarry (\fulladder_4_çarry ));
  FullAdder fulladder_5 (
    .A(DEC_out_10), .B(in_11), .Carry(\fulladder_2_çarry ), .S(fulladder_5_s), .\Çarry (\fulladder_5_çarry ));
  FullAdder fulladder_6 (
    .A(DEC_out_10), .B(comp2_1_out_10), .Carry(\fulladder_4_çarry ), .S(fulladder_6_s),
    .\Çarry (\fulladder_6_çarry ));
  FullAdder fulladder_7 (
    .A(DEC_out_11), .B(in_12), .Carry(\fulladder_5_çarry ), .S(fulladder_7_s), .\Çarry (\fulladder_7_çarry ));
  FullAdder fulladder_8 (.A(DEC_out_12), .B(in_13), .Carry(\fulladder_7_çarry ), .S(fulladder_8_s));  // open: Çarry
  FullAdder fulladder_9 (
    .A(DEC_out_11), .B(comp2_1_out_11), .Carry(\fulladder_6_çarry ), .S(fulladder_9_s),
    .\Çarry (\fulladder_9_çarry ));
  FullAdder fulladder_10 (
    .A(DEC_out_12), .B(comp2_1_out_12), .Carry(\fulladder_9_çarry ), .S(fulladder_10_s));  // open: Çarry
  not not_1 (not_1_out, in_1);
  and and_1 (and_1_out, halfadder_1_s, not_1_out);
  and and_2 (and_2_out, fulladder_1_s, not_1_out);
  and and_3 (and_3_out, fulladder_2_s, not_1_out);
  and and_4 (and_4_out, fulladder_5_s, not_1_out);
  and and_5 (and_5_out, fulladder_7_s, not_1_out);
  and and_6 (and_6_out, fulladder_8_s, not_1_out);
  and and_7 (and_7_out, halfadder_2_s, in_1);
  and and_8 (and_8_out, fulladder_3_s, in_1);
  and and_9 (and_9_out, fulladder_4_s, in_1);
  and and_10 (and_10_out, fulladder_6_s, in_1);
  and and_11 (and_11_out, fulladder_9_s, in_1);
  and and_12 (and_12_out, fulladder_10_s, in_1);
  or or_1 (out_14, and_1_out, and_7_out);
  or or_2 (out_15, and_2_out, and_8_out);
  or or_3 (out_16, and_3_out, and_9_out);
  or or_4 (out_17, and_4_out, and_10_out);
  or or_5 (out_18, and_5_out, and_11_out);
  or or_6 (out_19, and_6_out, and_12_out);
  Igual0 igual0_1 (
    .in_1(out_14), .in_2(out_15), .in_3(out_16), .in_4(out_17), .in_5(out_18), .in_6(out_19), .out_7(out_20));
endmodule

// C2
module Comp2 (
  input  in_1,
  input  in_2,
  input  in_3,
  input  in_4,
  input  in_5,
  input  in_6,
  output out_7,
  output out_8,
  output out_9,
  output out_10,
  output out_11,
  output out_12
);

  wire halfadder_1_carry, halfadder_2_carry, halfadder_3_carry, halfadder_4_carry, halfadder_5_carry,
       not_1_out, not_2_out, not_3_out, not_4_out, not_5_out, not_6_out, xor_1_out;

  not not_1 (not_1_out, in_1);
  xor xor_1 (xor_1_out, in_1, not_1_out);
  not not_2 (not_2_out, in_2);
  not not_3 (not_3_out, in_3);
  not not_4 (not_4_out, in_4);
  not not_5 (not_5_out, in_5);
  not not_6 (not_6_out, in_6);
  HalfAdder halfadder_1 (.A(xor_1_out), .B(not_1_out), .S(out_7), .Carry(halfadder_1_carry));
  HalfAdder halfadder_2 (.A(halfadder_1_carry), .B(not_2_out), .S(out_8), .Carry(halfadder_2_carry));
  HalfAdder halfadder_3 (.A(halfadder_2_carry), .B(not_3_out), .S(out_9), .Carry(halfadder_3_carry));
  HalfAdder halfadder_4 (.A(halfadder_3_carry), .B(not_4_out), .S(out_10), .Carry(halfadder_4_carry));
  HalfAdder halfadder_5 (.A(halfadder_4_carry), .B(not_5_out), .S(out_11), .Carry(halfadder_5_carry));
  HalfAdder halfadder_6 (.A(halfadder_5_carry), .B(not_6_out), .S(out_12));  // open: Carry
endmodule

// HA
module HalfAdder (
  input  A,
  input  B,
  output S,
  output Carry
);

  xor xor_1 (S, A, B);
  and and_1 (Carry, A, B);
endmodule

// FA
module FullAdder (
  input  A,
  input  B,
  input  Carry,
  output S,
  output \Çarry 
);

  wire and_1_out, and_2_out, and_3_out, xor_1_out;

  xor xor_1 (xor_1_out, A, B);
  and and_1 (and_1_out, A, Carry);
  and and_2 (and_2_out, A, B);
  or or_1 (\Çarry , and_1_out, and_2_out, and_3_out);
  and and_3 (and_3_out, B, Carry);
  xor xor_2 (S, xor_1_out, Carry);
endmodule

module Igual0 (
  input  in_1,
  input  in_2,
  input  in_3,
  input  in_4,
  input  in_5,
  input  in_6,
  output out_7
);

  wire or_1_out, or_2_out, or_3_out, or_4_out, or_5_out;

  or or_1 (or_1_out, in_1, in_2);
  or or_2 (or_2_out, in_3, in_4);
  or or_3 (or_3_out, in_5, in_6);
  or or_4 (or_4_out, or_1_out, or_2_out);
  or or_5 (or_5_out, or_4_out, or_3_out);
  not not_1 (out_7, or_5_out);
endmodule

module Inc1 (
  input  in_1,
  input  in_2,
  input  in_3,
  input  in_4,
  input  in_5,
  input  in_6,
  output out_7,
  output out_8,
  output out_9,
  output out_10,
  output out_11,
  output out_12
);

  wire halfadder_1_carry, halfadder_2_carry, halfadder_3_carry, halfadder_4_carry, halfadder_5_carry,
       not_1_out, or_1_out;

  not not_1 (not_1_out, in_1);
  or or_1 (or_1_out, not_1_out, in_1);
  HalfAdder halfadder_1 (.A(or_1_out), .B(in_1), .S(out_7), .Carry(halfadder_1_carry));
  HalfAdder halfadder_2 (.A(in_2), .B(halfadder_1_carry), .S(out_8), .Carry(halfadder_2_carry));
  HalfAdder halfadder_3 (.A(in_3), .B(halfadder_2_carry), .S(out_9), .Carry(halfadder_3_carry));
  HalfAdder halfadder_4 (.A(in_4), .B(halfadder_3_carry), .S(out_10), .Carry(halfadder_4_carry));
  HalfAdder halfadder_5 (.A(in_5), .B(halfadder_4_carry), .S(out_11), .Carry(halfadder_5_carry));
  HalfAdder halfadder_6 (.A(in_6), .B(halfadder_5_carry), .S(out_12));  // open: Carry
endmodule

module Dec1 (
  input  in_1,
  input  in_2,
  input  in_3,
  input  in_4,
  input  in_5,
  input  in_6,
  output out_7,
  output out_8,
  output out_9,
  output out_10,
  output out_11,
  output out_12
);

  wire \fulladder_1_çarry , \fulladder_2_çarry , \fulladder_3_çarry , \fulladder_4_çarry , halfadder_1_carry,
       not_1_out, or_1_out;

  not not_1 (not_1_out, in_1);
  or or_1 (or_1_out, in_1, not_1_out);
  HalfAdder halfadder_1 (.A(or_1_out), .B(in_1), .S(out_7), .Carry(halfadder_1_carry));
  FullAdder fulladder_1 (.A(in_2), .B(or_1_out), .Carry(halfadder_1_carry), .S(out_8), .\Çarry (\fulladder_1_çarry ));
  FullAdder fulladder_2 (.A(or_1_out), .B(in_3), .Carry(\fulladder_1_çarry ), .S(out_9), .\Çarry (\fulladder_2_çarry ));
  FullAdder fulladder_3 (
    .A(or_1_out), .B(in_4), .Carry(\fulladder_2_çarry ), .S(out_10), .\Çarry (\fulladder_3_çarry ));
  FullAdder fulladder_4 (
    .A(or_1_out), .B(in_5), .Carry(\fulladder_3_çarry ), .S(out_11), .\Çarry (\fulladder_4_çarry ));
  FullAdder fulladder_5 (.A(or_1_out), .B(in_6), .Carry(\fulladder_4_çarry ), .S(out_12));  // open: Çarry
endmodule
