// Logisim project Exemplo0035.circ as structural Verilog: 1 circuit, main circuit main
module main (
  input  a,
  input  b,
  output a___b,
  output a___b_2,
  output a___b_3
);

  wire n1_out, n2_out;

  not n1 (n1_out, a);
  not n2 (n2_out, b);
  and s0 (a___b, n1_out, b);
  xnor s1 (a___b_2, a, b);
  and s2 (a___b_3, a, n2_out);
endmodule
