// Logisim project Ex02.circ as structural Verilog: 4 circuits, main circuit main
module main (
  input  [5:0] in_1,
  input  [5:0] in_2,
  input  in_3,
  output out_4,
  output out_5,
  output out_6,
  output out_7,
  output out_8,
  output out_9,
  output out_10,
  output out_11
);

  wire sumsubtcompleto_1_out_6, sumsubtcompleto_2_out_6, sumsubtcompleto_3_out_6, sumsubtcompleto_4_out_6,
       sumsubtcompleto_5_out_6;

  SumSubtCompleto sumsubtcompleto_1 (
    .a(in_3), .b(in_1[0]), .sel(in_2[0]), .cin(in_3), .out_5(out_4), .out_6(sumsubtcompleto_1_out_6));
  SumSubtCompleto sumsubtcompleto_2 (
    .a(in_1[1]), .b(in_2[1]), .sel(sumsubtcompleto_1_out_6), .cin(in_3), .out_5(out_5),
    .out_6(sumsubtcompleto_2_out_6));
  SumSubtCompleto sumsubtcompleto_3 (
    .a(in_1[2]), .b(in_2[2]), .sel(sumsubtcompleto_2_out_6), .cin(in_3), .out_5(out_6),
    .out_6(sumsubtcompleto_3_out_6));
  SumSubtCompleto sumsubtcompleto_4 (
    .a(in_1[3]), .b(in_2[3]), .sel(sumsubtcompleto_3_out_6), .cin(in_3), .out_5(out_8),
    .out_6(sumsubtcompleto_4_out_6));
  SumSubtCompleto sumsubtcompleto_5 (
    .a(in_1[4]), .b(in_2[4]), .sel(sumsubtcompleto_4_out_6), .cin(in_3), .out_5(out_9),
    .out_6(sumsubtcompleto_5_out_6));
  SumSubtCompleto sumsubtcompleto_6 (
    .a(in_1[5]), .b(in_2[5]), .sel(sumsubtcompleto_5_out_6), .cin(in_3), .out_5(out_10), .out_6(out_11));
  nor nor_1 (out_7, out_4, out_5, out_6, out_8, out_9, out_10);
endmodule

module Sum (
  input  a,
  input  b,
  output s,
  output s1
);

  xor xor_1 (s, a, b);
  and and_1 (s1, a, b);
endmodule

module SumCompleta (
  input  CarryIn,
  input  a,
  input  b,
  output out_4,
  output out_5
);

  wire sum_1_s, sum_1_s1, sum_2_s1;

  Sum sum_1 (.a(a), .b(b), .s(sum_1_s), .s1(sum_1_s1));
  Sum sum_2 (.a(CarryIn), .b(sum_1_s), .s(out_4), .s1(sum_2_s1));
  or or_1 (out_5, sum_2_s1, sum_1_s1);
endmodule

module SumSubtCompleto (
  input  a,
  input  b,
  input  sel,
  input  cin,
  output out_5,
  output out_6
);

  wire xor_1_out;

  xor xor_1 (xor_1_out, b, sel);
  SumCompleta sumcompleta_1 (.CarryIn(a), .a(xor_1_out), .b(cin), .out_4(out_5), .out_5(out_6));
endmodule
