// Logisim project Exercicio01.circ as structural Verilog: 1 circuit, main circuit main
module main (
  input  a,
  input  b,
  input  carry_in,
  input  sinal,
  output out_5,
  output out_6
);

  wire and_1_out, and_2_out, or_1_out, xor_1_out, xor_2_out;

  xor xor_1 (xor_1_out, a, b);
  and and_1 (and_1_out, b, carry_in);
  xor xor_2 (xor_2_out, sinal, a);
  or or_1 (or_1_out, b, carry_in);
  and and_2 (and_2_out, xor_2_out, or_1_out);
  or or_2 (out_6, and_1_out, and_2_out);
  xor xor_3 (out_5, xor_1_out, carry_in);

  // Notes on the sheet:
  //   LUIZ MARQUES DE OLIVEIRA - 417138
endmodule
