// Logisim project guia05.circ as structural Verilog
// HA
module HALF_ADDER (
  input  Y,
  input  X,
  output S,
  output C_OUT
);

  xor xor_1 (S, Y, X);
  and and_1 (C_OUT, Y, X);

  // Notes on the sheet:
  //   HALF ADDER 2 BITS
endmodule

// FA
module FULL_ADDER (
  input  C_IN,
  input  X,
  input  Y,
  output S,
  output C_OUT
);

  wire half_adder_1_c_out, half_adder_1_s, half_adder_2_c_out;

  HALF_ADDER half_adder_1 (.Y(X), .X(Y), .C_OUT(half_adder_1_c_out), .S(half_adder_1_s));
  HALF_ADDER half_adder_2 (.Y(C_IN), .X(half_adder_1_s), .C_OUT(half_adder_2_c_out), .S(S));
  or or_1 (C_OUT, half_adder_2_c_out, half_adder_1_c_out);

  // Notes on the sheet:
  //   FULL ADDER 2 BITS
endmodule

// UA
module Exemplo0031 (
  input  OP,
  input  Sinal_B,
  input  B4,
  input  B3,
  input  B2,
  input  B1,
  input  B0,
  input  Sinal_A,
  input  A4,
  input  A3,
  input  A2,
  input  A1,
  input  A0,
  output S0,
  output S1,
  output S2,
  output S3,
  output S4,
  output Sinal
);

  wire full_adder_2_c_out, full_adder_3_c_out, full_adder_4_c_out, full_adder_5_c_out, full_adder_6_c_out,
       xor_1_out, xor_2_out, xor_3_out, xor_4_out, xor_5_out, xor_6_out;

  FULL_ADDER full_adder_1 (.C_IN(full_adder_2_c_out), .X(Sinal_A), .Y(xor_1_out), .S(Sinal));  // open: C_OUT
  xor xor_1 (xor_1_out, Sinal_B, OP);
  FULL_ADDER full_adder_2 (.C_IN(full_adder_3_c_out), .X(A4), .Y(xor_2_out), .S(S4), .C_OUT(full_adder_2_c_out));
  xor xor_2 (xor_2_out, B4, OP);
  FULL_ADDER full_adder_3 (.C_IN(full_adder_4_c_out), .X(A3), .Y(xor_4_out), .S(S3), .C_OUT(full_adder_3_c_out));
  xor xor_3 (xor_3_out, B2, OP);
  xor xor_4 (xor_4_out, B3, OP);
  FULL_ADDER full_adder_4 (.C_IN(full_adder_5_c_out), .X(A2), .Y(xor_3_out), .S(S2), .C_OUT(full_adder_4_c_out));
  xor xor_5 (xor_5_out, B1, OP);
  FULL_ADDER full_adder_5 (.C_IN(full_adder_6_c_out), .X(A1), .Y(xor_5_out), .S(S1), .C_OUT(full_adder_5_c_out));
  xor xor_6 (xor_6_out, B0, OP);
  FULL_ADDER full_adder_6 (.C_IN(OP), .X(A0), .Y(xor_6_out), .S(S0), .C_OUT(full_adder_6_c_out));
endmodule

module Equals_0 (
  input  Sinal_A,
  input  A4,
  input  A3,
  input  A2,
  input  A1,
  input  A0,
  output S
);

  wire or_1_out;

  not not_1 (S, or_1_out);
  or or_1 (or_1_out, Sinal_A, A4, A3, A2, A1, A0);
endmodule

module Exemplo0032 (
  input  Sinal_A,
  input  A4,
  input  A3,
  input  A2,
  input  A1,
  input  A0,
  input  OP,
  input  Sinal_B,
  input  B4,
  input  B3,
  input  B2,
  input  B1,
  input  B0,
  output Sinal,
  output S4,
  output S3,
  output S2,
  output S1,
  output S0,
  output _0
);

  Exemplo0031 exemplo0031_1 (
    .S0(S0), .S1(S1), .S2(S2), .S3(S3), .S4(S4), .Sinal(Sinal), .Sinal_B(Sinal_B), .B4(B4), .B3(B3), .B2(B2),
    .B1(B1), .B0(B0), .Sinal_A(Sinal_A), .A4(A4), .A3(A3), .A2(A2), .A1(A1), .A0(A0), .OP(OP));
  Equals_0 equals_0_1 (.Sinal_A(Sinal), .A4(S4), .A3(S3), .A2(S2), .A1(S1), .A0(S0), .S(_0));
endmodule

module _1 (
  input  Sinal_A,
  input  A4,
  input  A3,
  input  A2,
  input  A1,
  input  A0,
  output Sinal,
  output S4,
  output S3,
  output S2,
  output S1,
  output S0
);

  Exemplo0031 exemplo0031_1 (
    .S0(S0), .S1(S1), .S2(S2), .S3(S3), .S4(S4), .Sinal(Sinal), .Sinal_B(1'b0), .B4(1'b0), .B3(1'b0),
    .B2(1'b0), .B1(1'b0), .B0(1'b1), .Sinal_A(Sinal_A), .A4(A4), .A3(A3), .A2(A2), .A1(A1), .A0(A0), .OP(1'b0));
endmodule

module Exemplo0033 (
  input  Sinal_A,
  input  A4,
  input  A3,
  input  A2,
  input  A1,
  input  A0,
  input  OP,
  input  Sinal_B,
  input  B4,
  input  B3,
  input  B2,
  input  B1,
  input  B0,
  output Sinal,
  output S4,
  output S3,
  output S2,
  output S1,
  output S0,
  output _0,
  output Sinal_2,
  output S4_2,
  output S3_2,
  output S2_2,
  output S1_2,
  output S0_2
);

  Exemplo0031 exemplo0031_1 (
    .S0(S0), .S1(S1), .S2(S2), .S3(S3), .S4(S4), .Sinal(Sinal), .Sinal_B(Sinal_B), .B4(B4), .B3(B3), .B2(B2),
    .B1(B1), .B0(B0), .Sinal_A(Sinal_A), .A4(A4), .A3(A3), .A2(A2), .A1(A1), .A0(A0), .OP(OP));
  _1 u_1_1 (
    .Sinal_A(Sinal), .A4(S4), .A3(S3), .A2(S2), .A1(S1), .A0(S0), .Sinal(Sinal_2), .S4(S4_2), .S3(S3_2),
    .S2(S2_2), .S1(S1_2), .S0(S0_2));
  Equals_0 equals_0_1 (.Sinal_A(Sinal), .A4(S4), .A3(S3), .A2(S2), .A1(S1), .A0(S0), .S(_0));
endmodule

module _1_2 (
  input  Sinal_A,
  input  A4,
  input  A3,
  input  A2,
  input  A1,
  input  A0,
  output Sinal,
  output S4,
  output S3,
  output S2,
  output S1,
  output S0
);

  Exemplo0031 exemplo0031_1 (
    .S0(S0), .S1(S1), .S2(S2), .S3(S3), .S4(S4), .Sinal(Sinal), .Sinal_B(1'b0), .B4(1'b0), .B3(1'b0),
    .B2(1'b0), .B1(1'b0), .B0(1'b1), .Sinal_A(Sinal_A), .A4(A4), .A3(A3), .A2(A2), .A1(A1), .A0(A0), .OP(1'b1));
endmodule

module Exemplo0034 (
  input  Sinal_A,
  input  A4,
  input  A3,
  input  A2,
  input  A1,
  input  A0,
  input  OP,
  input  Sinal_B,
  input  B4,
  input  B3,
  input  B2,
  input  B1,
  input  B0,
  output Sinal,
  output S4,
  output S3,
  output S2,
  output S1,
  output S0,
  output _0,
  output Sinal_2,
  output S4_2,
  output S3_2,
  output S2_2,
  output S1_2,
  output S0_2,
  output Sinal_3,
  output S4_3,
  output S3_3,
  output S2_3,
  output S1_3,
  output S0_3
);

  Exemplo0031 exemplo0031_1 (
    .S0(S0), .S1(S1), .S2(S2), .S3(S3), .S4(S4), .Sinal(Sinal), .Sinal_B(Sinal_B), .B4(B4), .B3(B3), .B2(B2),
    .B1(B1), .B0(B0), .Sinal_A(Sinal_A), .A4(A4), .A3(A3), .A2(A2), .A1(A1), .A0(A0), .OP(OP));
  _1 u_1_1 (
    .Sinal_A(Sinal), .A4(S4), .A3(S3), .A2(S2), .A1(S1), .A0(S0), .Sinal(Sinal_2), .S4(S4_2), .S3(S3_2),
    .S2(S2_2), .S1(S1_2), .S0(S0_2));
  _1_2 u_1_2 (
    .Sinal_A(Sinal), .A4(S4), .A3(S3), .A2(S2), .A1(S1), .A0(S0), .Sinal(Sinal_3), .S4(S4_3), .S3(S3_3),
    .S2(S2_3), .S1(S1_3), .S0(S0_3));
  Equals_0 equals_0_1 (.Sinal_A(Sinal), .A4(S4), .A3(S3), .A2(S2), .A1(S1), .A0(S0), .S(_0));
endmodule

module Comparador (
  input  Sinal_A,
  input  A4,
  input  A3,
  input  A2,
  input  A1,
  input  A0,
  input  Sinal_B,
  input  B4,
  input  B3,
  input  B2,
  input  B1,
  input  B0,
  output A___B,
  output A___B_2
);

  Exemplo0031 exemplo0031_1 (
    .Sinal(A___B), .Sinal_B(Sinal_B), .B4(B4), .B3(B3), .B2(B2), .B1(B1), .B0(B0), .Sinal_A(Sinal_A),
    .A4(A4), .A3(A3), .A2(A2), .A1(A1), .A0(A0), .OP(1'b1));  // open: S0, S1, S2, S3, S4
  not not_1 (A___B_2, A___B);
endmodule

module Exemplo0035 (
  input  Sinal_A,
  input  A4,
  input  A3,
  input  A2,
  input  A1,
  input  A0,
  input  Sinal_B,
  input  B4,
  input  B3,
  input  B2,
  input  B1,
  input  B0,
  output A___B,
  output A___B_2
);

  Comparador comparador_1 (
    .Sinal_A(A0), .A4(A1), .A3(A2), .A2(A3), .A1(A4), .A0(Sinal_A), .Sinal_B(B0), .B4(B1), .B3(B2), .B2(B3),
    .B1(B4), .B0(Sinal_B), .A___B(A___B), .A___B_2(A___B_2));
endmodule
