// Logisim project Exemplo0031.circ as structural Verilog: 1 circuit, main circuit main
module main (
  input  [5:0] X,
  input  [5:0] Y,
  input  [5:0] X_2,
  input  [5:0] Y_2,
  output [5:0] out_5,
  output [5:0] S,
  output [5:0] out_7
);

  wire [5:0] and_1_out, and_2_out, and_3_out, and_4_out, not_2_out, or_1_out, or_2_out, or_3_out, undriven,
       undriven_2, xor_1_out;

  assign X_2 = ~X_2;  // NOT_Gate not_1, 6 bits wide
  assign or_1_out = X | Y;  // OR_Gate or_1, 6 bits wide
  assign and_1_out = Y & X;  // AND_Gate and_1, 6 bits wide
  assign xor_1_out = X_2 ^ Y_2;  // XOR_Gate xor_1, 6 bits wide
  assign and_2_out = Y_2 & X_2;  // AND_Gate and_2, 6 bits wide
  assign not_2_out = ~xor_1_out;  // NOT_Gate not_2, 6 bits wide
  assign out_5 = undriven_2 ^ or_1_out;  // XOR_Gate xor_2, 6 bits wide
  assign and_3_out = or_1_out & undriven_2;  // AND_Gate and_3, 6 bits wide
  assign and_4_out = undriven & not_2_out;  // AND_Gate and_4, 6 bits wide
  assign or_2_out = and_3_out | and_1_out;  // OR_Gate or_2, 6 bits wide
  assign out_7 = undriven ^ xor_1_out;  // XOR_Gate xor_3, 6 bits wide
  assign or_3_out = and_4_out | and_2_out;  // OR_Gate or_3, 6 bits wide
  assign S = or_2_out & or_3_out;  // AND_Gate and_5, 6 bits wide

  // Notes on the sheet:
  //   Vai Um
  //   Vai um
  //   Subtrator
  //   Somador
  //   Saída
endmodule
