// Logisim project Guia05.circ as structural Verilog: 5 circuits, main circuit main
module main (
  input  [5:0] A,
  input  [5:0] B,
  output A_B,
  output A_B_2,
  output A_B_3
);

  Entrada_Bits entrada_bits_1 (
    .a0(A[5]), .b0(B[5]), .a1(A[4]), .b1(B[4]), .a2(A[3]), .b2(B[3]), .a3(A[2]), .b3(B[2]), .a4(A[1]),
    .b4(B[1]), .a5(A[0]), .b5(B[0]), .s(A_B), .s1(A_B_2), .s2(A_B_3));
endmodule

module Entrada_Bits (
  input  a0,
  input  b0,
  input  a1,
  input  b1,
  input  a2,
  input  b2,
  input  a3,
  input  b3,
  input  a4,
  input  b4,
  input  a5,
  input  b5,
  output s,
  output s1,
  output s2
);

  wire igual_1_s, igual_1_t, igual_1_u, igual_1_v, igual_1_w, igual_1_x, maiormenor_1_s;

  Igual igual_1 (
    .A0(a0), .B0(b0), .A1(a1), .B1(b1), .A2(a2), .B2(b2), .A3(a3), .B3(b3), .A4(a4), .B4(b4), .A5(a5),
    .B5(b5), .s(igual_1_s), .t(igual_1_t), .u(igual_1_u), .v(igual_1_v), .w(igual_1_w), .x(igual_1_x));
  MaiorMenor maiormenor_1 (
    .A0(a0), .B0(b0), .A1(a1), .B1(b1), .A2(a2), .B2(b2), .A3(a3), .B3(b3), .A4(a4), .B4(b4), .A5(a5),
    .B5(b5), .c(igual_1_x), .d(igual_1_w), .e(igual_1_v), .f(igual_1_u), .g(igual_1_t), .s(maiormenor_1_s));
  Magnitude magnitude_1 (.a(igual_1_s), .b(maiormenor_1_s), .s(s), .t(s1), .u(s2));
endmodule

module Igual (
  input  A0,
  input  B0,
  input  A1,
  input  B1,
  input  A2,
  input  B2,
  input  A3,
  input  B3,
  input  A4,
  input  B4,
  input  A5,
  input  B5,
  output s,
  output t,
  output u,
  output v,
  output w,
  output x
);

  wire xnor2_out, xnor3_out, xnor4_out, xnor5_out, xnor6_out;

  xnor xnor1 (x, A0, B0);
  xnor xnor2 (xnor2_out, A1, B1);
  xnor xnor3 (xnor3_out, A2, B2);
  xnor xnor4 (xnor4_out, A3, B3);
  xnor xnor5 (xnor5_out, A4, B4);
  xnor xnor6 (xnor6_out, A5, B5);
  and and1 (w, x, xnor2_out);
  and and2 (v, w, xnor3_out);
  and and3 (u, v, xnor4_out);
  and and4 (t, u, xnor5_out);
  and and5 (s, t, xnor6_out);
endmodule

module MaiorMenor (
  input  c,
  input  d,
  input  e,
  input  f,
  input  g,
  input  A0,
  input  B0,
  input  A1,
  input  B1,
  input  A2,
  input  B2,
  input  A3,
  input  B3,
  input  A4,
  input  B4,
  input  A5,
  input  B5,
  output s
);

  wire a10_out, a11_out, and1_out, and2_out, and3_out, and4_out, and5_out, and6_out, and7_out, and8_out,
       and9_out, not_1_out, not_2_out, not_3_out, not_4_out, not_5_out, not_6_out, or1_out, or2_out, or3_out,
       or4_out;

  and and1 (and1_out, A0, not_1_out);
  not not_1 (not_1_out, B0);
  and and2 (and2_out, A1, not_2_out);
  not not_2 (not_2_out, B1);
  and and3 (and3_out, A2, not_3_out);
  not not_3 (not_3_out, B2);
  and and4 (and4_out, A3, not_4_out);
  not not_4 (not_4_out, B3);
  and and5 (and5_out, A4, not_5_out);
  not not_5 (not_5_out, B4);
  and and6 (and6_out, A5, not_6_out);
  not not_6 (not_6_out, B5);
  and and7 (and7_out, c, and2_out);
  and and8 (and8_out, d, and3_out);
  or or1 (or1_out, and7_out, and1_out);
  and and9 (and9_out, e, and4_out);
  and a10 (a10_out, f, and5_out);
  or or3 (or3_out, and9_out, or2_out);
  or or2 (or2_out, and8_out, or1_out);
  and a11 (a11_out, g, and6_out);
  or or4 (or4_out, a10_out, or3_out);
  or or5 (s, a11_out, or4_out);
endmodule

module Magnitude (
  input  a,
  input  b,
  output s,
  output t,
  output u
);

  wire not1_out, not2_out;

  not not1 (not1_out, a);
  not not2 (not2_out, b);
  and and1 (u, not1_out, not2_out);

  assign s = a;
  assign t = b;
endmodule
