// Logisim project Exemplo0051.circ as structural Verilog: 3 circuits, main circuit soma_completa
// add
module soma_completa (
  input  Carry_In,
  input  x,
  input  y,
  output S,
  output Carry_Out
);

  wire AND2_out, AND_1_out, XOR1_out;

  xor XOR1 (XOR1_out, x, y);
  and AND_1 (AND_1_out, y, x);
  and AND2 (AND2_out, Carry_In, XOR1_out);
  xor XOR2 (S, Carry_In, XOR1_out);
  or OR1 (Carry_Out, AND2_out, AND_1_out);

  // Notes on the sheet:
  //   w1
  //   w2
  //   w3
endmodule

// add
module full_add_chave (
  input  x,
  input  y,
  input  carry_in,
  input  chave,
  output saida,
  output carry_out
);

  wire xor1_out;

  xor xor1 (xor1_out, y, chave);
  soma_completa soma_completa_1 (.Carry_In(carry_in), .x(x), .y(xor1_out), .S(saida), .Carry_Out(carry_out));

  // Notes on the sheet:
  //   w1
endmodule

module ex (
  input  [5:0] x,
  input  [5:0] y,
  input  chave,
  output s0,
  output s1,
  output s2,
  output s3,
  output s4,
  output s5,
  output Carry_Out
);

  wire full_add_chave_1_carry_out, full_add_chave_2_carry_out, full_add_chave_3_carry_out,
       full_add_chave_4_carry_out, full_add_chave_5_carry_out, full_add_chave_6_carry_out;

  full_add_chave full_add_chave_1 (
    .x(x[0]), .y(y[0]), .carry_in(chave), .chave(chave), .saida(s0), .carry_out(full_add_chave_1_carry_out));
  full_add_chave full_add_chave_2 (
    .x(x[1]), .y(y[1]), .carry_in(full_add_chave_1_carry_out), .chave(chave), .saida(s1),
    .carry_out(full_add_chave_2_carry_out));
  full_add_chave full_add_chave_3 (
    .x(x[2]), .y(y[3]), .carry_in(full_add_chave_2_carry_out), .chave(chave), .saida(s2),
    .carry_out(full_add_chave_3_carry_out));
  full_add_chave full_add_chave_4 (
    .x(x[3]), .y(y[2]), .carry_in(full_add_chave_3_carry_out), .chave(chave), .saida(s3),
    .carry_out(full_add_chave_4_carry_out));
  full_add_chave full_add_chave_5 (
    .x(x[4]), .y(y[4]), .carry_in(full_add_chave_4_carry_out), .chave(chave), .saida(s4),
    .carry_out(full_add_chave_5_carry_out));
  full_add_chave full_add_chave_6 (
    .x(x[5]), .y(y[5]), .carry_in(full_add_chave_5_carry_out), .chave(chave), .saida(s5),
    .carry_out(full_add_chave_6_carry_out));
  xor xor_1 (Carry_Out, full_add_chave_6_carry_out, chave);

  // Notes on the sheet:
  //   Mateus Augusto Moraes Ferreira    Matricula: 435669
  //   soma=0  
  //   subtração=1
  //   w1
  //   w2
  //   w3
  //   w4
  //   w5
  //   w6
endmodule
