// Logisim project Exemplo0053.circ as structural Verilog: 5 circuits, main circuit exemplo0053
module exemplo0053 (
  input  [5:0] in_1,
  input  [5:0] in_2,
  input  in_3,
  input  [5:0] in_4,
  output Carry_Out,
  output [5:0] out_6
);

  wire [5:0] circuito_1_out_5;

  somacompleta6 somacompleta6_1 (
    .in_1(in_4), .in_2(circuito_1_out_5), .s0(out_6[5]), .s1(out_6[4]), .s2(out_6[3]), .s3(out_6[2]),
    .s4(out_6[1]), .s5(out_6[0]), .Chave(in_3), .Carry_Out(Carry_Out));
  circuito circuito_1 (.out_5(circuito_1_out_5), .in_1(in_3), .in_2(in_1), .in_3(in_2));  // open: out_4

  // Notes on the sheet:
  //   Mateus Augusto Moraes Ferreira   Matricula: 435669
  //   soma = carryIn = 0
  //   subtraçao = carryIn = 1
endmodule

// soma6
module somacompleta6 (
  input  [5:0] in_1,
  input  [5:0] in_2,
  input  Chave,
  output s0,
  output s1,
  output s2,
  output s3,
  output s4,
  output s5,
  output Carry_Out
);

  wire somachave_1_s1, somachave_2_s1, somachave_3_s1, somachave_4_s1, somachave_6_s1;

  somachave somachave_1 (.x(in_1[0]), .y(in_2[0]), .Carry_in(Chave), .Chave(Chave), .s0(s0), .s1(somachave_1_s1));
  somachave somachave_2 (
    .x(in_1[1]), .y(in_2[1]), .Carry_in(somachave_1_s1), .Chave(Chave), .s0(s1), .s1(somachave_2_s1));
  somachave somachave_3 (
    .x(in_1[2]), .y(in_2[2]), .Carry_in(somachave_2_s1), .Chave(Chave), .s0(s2), .s1(somachave_3_s1));
  somachave somachave_4 (
    .x(in_1[3]), .y(in_2[3]), .Carry_in(somachave_3_s1), .Chave(Chave), .s0(s3), .s1(somachave_4_s1));
  somachave somachave_5 (.x(in_1[4]), .y(in_2[4]), .Carry_in(somachave_4_s1), .Chave(Chave), .s0(s4));  // open: s1
  somachave somachave_6 (.x(in_1[5]), .y(in_2[5]), .Carry_in(Chave), .Chave(Chave), .s0(s5), .s1(somachave_6_s1));
  xor xor1 (Carry_Out, Chave, somachave_6_s1);

  // Notes on the sheet:
  //   soma=0
  //   subtracao=1
endmodule

module somacompleta (
  input  carry_In,
  input  x,
  input  y,
  output s0,
  output carry_out
);

  wire and1_out, and2_out, xor1_out;

  xor xor1 (xor1_out, x, y);
  and and1 (and1_out, x, y);
  xor xor2 (s0, carry_In, xor1_out);
  and and2 (and2_out, carry_In, xor1_out);
  or or1 (carry_out, and2_out, and1_out);
endmodule

// add
module somachave (
  input  x,
  input  y,
  input  Carry_in,
  input  Chave,
  output s0,
  output s1
);

  wire xor_1_out;

  xor xor_1 (xor_1_out, y, Chave);
  somacompleta somacompleta_1 (.carry_In(Carry_in), .x(x), .y(xor_1_out), .s0(s0), .carry_out(s1));
endmodule

// circ
module circuito (
  input  in_1,
  input  [5:0] in_2,
  input  [5:0] in_3,
  output out_4,
  output [5:0] out_5
);

  somacompleta6 somacompleta6_1 (
    .in_1(in_3), .in_2(in_2), .s0(out_5[5]), .s1(out_5[4]), .s2(out_5[3]), .s3(out_5[2]), .s4(out_5[1]),
    .s5(out_5[0]), .Chave(in_1), .Carry_Out(out_4));
endmodule
