// Logisim project Exemplo0055.circ as structural Verilog: 4 circuits, main circuit exemplo0055
module exemplo0055 (
  input  [5:0] x,
  input  [5:0] y,
  input  chave1,
  input  chave2,
  output s
);

  wire and1_out, and3_2_out, and3_out, igual_1_s, maior_1_s, menor_1_s, not_1_out, not_2_out, not_3_out,
       not_4_out, or1_out;

  igual igual_1 (.x(x), .y(y), .s(igual_1_s));
  maior maior_1 (.x(x), .y(y), .s(maior_1_s));
  menor menor_1 (.x(x), .y(y), .s(menor_1_s));
  not not_1 (not_1_out, chave1);
  not not_2 (not_2_out, chave2);
  not not_3 (not_3_out, chave1);
  not not_4 (not_4_out, chave2);
  and and3 (and3_out, menor_1_s, not_4_out, chave1);
  and and1 (and1_out, igual_1_s, not_1_out, not_2_out);
  and and3_2 (and3_2_out, maior_1_s, chave2, not_3_out);
  or or1 (or1_out, and1_out, and3_2_out);
  or or2 (s, or1_out, and3_out);

  // Notes on the sheet:
  //   igual
  //   maior
  //   menor
  //   Mateus Augusto Moraes Ferreira Matricula:435669
endmodule

// >
module maior (
  input  [5:0] x,
  input  [5:0] y,
  output s
);

  wire and1_out, and2_2_out, and2_out, and3_out, and4_out, and5_out, not_1_out, not_2_out, not_3_out,
       not_4_out, not_5_out, not_6_out, or1_out, or2_out, or3_out, or4_out;

  not not_1 (not_1_out, x[0]);
  not not_2 (not_2_out, x[1]);
  and and1 (and1_out, not_1_out, y[0]);
  or or1 (or1_out, and1_out, and2_out);
  or or5 (s, or3_out, or4_out);
  not not_3 (not_3_out, x[2]);
  and and2 (and2_out, not_2_out, y[1]);
  or or4 (or4_out, or1_out, or2_out);
  not not_4 (not_4_out, x[3]);
  and and3 (and3_out, not_4_out, y[3]);
  and and2_2 (and2_2_out, not_3_out, y[2]);
  or or2 (or2_out, and2_2_out, and3_out);
  not not_5 (not_5_out, x[4]);
  and and4 (and4_out, not_5_out, y[4]);
  not not_6 (not_6_out, x[5]);
  and and5 (and5_out, not_6_out, y[5]);
  or or3 (or3_out, and4_out, and5_out);

  // Notes on the sheet:
  //   Mateus Augusto Moraes Ferreira Matricula:435669
endmodule

// <
module menor (
  input  [5:0] x,
  input  [5:0] y,
  output s
);

  wire and1_out, and2_2_out, and2_out, and3_out, and4_out, and5_out, not_1_out, not_2_out, not_3_out,
       not_4_out, not_5_out, not_6_out, or1_out, or2_out, or3_out, or4_out;

  not not_1 (not_1_out, y[0]);
  and and1 (and1_out, x[0], not_1_out);
  not not_2 (not_2_out, y[1]);
  or or1 (or1_out, and1_out, and2_out);
  or or5 (s, or3_out, or4_out);
  and and2 (and2_out, x[1], not_2_out);
  not not_3 (not_3_out, y[2]);
  or or4 (or4_out, or1_out, or2_out);
  and and3 (and3_out, x[3], not_4_out);
  and and2_2 (and2_2_out, x[2], not_3_out);
  not not_4 (not_4_out, y[3]);
  or or2 (or2_out, and2_2_out, and3_out);
  and and4 (and4_out, x[4], not_5_out);
  not not_5 (not_5_out, y[4]);
  and and5 (and5_out, x[5], not_6_out);
  not not_6 (not_6_out, y[5]);
  or or3 (or3_out, and4_out, and5_out);

  // Notes on the sheet:
  //   Mateus Augusto Moraes Ferreira Matricula:435669
endmodule

// =
module igual (
  input  [5:0] x,
  input  [5:0] y,
  output s
);

  wire and1_out, and2_out, and3_out, and4_out, xor1_out, xor2_out, xor3_out, xor4_out, xor5_out, xor6_out;

  xnor xor1 (xor1_out, x[0], y[0]);
  and and1 (and1_out, xor1_out, xor2_out);
  and and5 (s, and3_out, and4_out);
  xnor xor2 (xor2_out, x[1], y[1]);
  and and4 (and4_out, and1_out, and2_out);
  xnor xor3 (xor3_out, x[2], y[2]);
  and and2 (and2_out, xor3_out, xor4_out);
  xnor xor4 (xor4_out, x[3], y[3]);
  xnor xor6 (xor6_out, x[5], y[5]);
  xnor xor5 (xor5_out, x[4], y[4]);
  and and3 (and3_out, xor5_out, xor6_out);

  // Notes on the sheet:
  //   Mateus Augusto Moreas Ferreira Matricula:435669
endmodule
