// Logisim project circuitos05.circ as structural Verilog: 9 circuits, main circuit MeiaSoma
module MeiaSoma (
  input  a,
  input  b,
  output carry,
  output s0
);

  and and_1 (carry, a, b);
  xor xor_1 (s0, a, b);
endmodule

module SomadorCompleto (
  input  a,
  input  b,
  input  carry_in,
  output carry,
  output s0
);

  wire meiasoma_1_carry, meiasoma_1_s0, meiasoma_2_carry;

  MeiaSoma meiasoma_1 (.a(a), .b(b), .carry(meiasoma_1_carry), .s0(meiasoma_1_s0));
  MeiaSoma meiasoma_2 (.a(carry_in), .b(meiasoma_1_s0), .carry(meiasoma_2_carry), .s0(s0));
  or or_1 (carry, meiasoma_1_carry, meiasoma_2_carry);
endmodule

module Ex02 (
  input  Sinal_A,
  input  Sinal_B,
  input  A4,
  input  B4,
  input  A3,
  input  B3,
  input  A2,
  input  B2,
  input  A1,
  input  B1,
  input  A0,
  input  B0,
  input  Chave,
  output carry,
  output s5,
  output s4,
  output s3,
  output s2,
  output s1,
  output s0,
  output Igual_a_zero
);

  Ex01 ex01_1 (
    .Chave(Chave), .B0(B0), .A0(A0), .B1(B1), .A1(A1), .B2(B2), .A2(A2), .B3(B3), .A3(A3), .B4(B4), .A4(A4),
    .Sinal_B(Sinal_B), .Sinal_A(Sinal_A), .s0(s0), .s1(s1), .s2(s2), .s3(s3), .s4(s4), .s5(s5), .carry(carry));
  and and_1 (Igual_a_zero, s0, s1, s2, s3, s4, s5, carry);

  // Notes on the sheet:
  //   Somador/Subtrator e flag igual a zero
endmodule

module Igualdade (
  input  in_1,
  input  in_2,
  output out_3
);

  xnor xnor_1 (out_3, in_2, in_1);
endmodule

module Ex03 (
  input  Sinal_B,
  input  Chave,
  input  B0,
  input  A0,
  input  B1,
  input  A1,
  input  B2,
  input  A2,
  input  B3,
  input  A3,
  input  B4,
  input  A4,
  input  Sinal_A,
  output s0,
  output s1,
  output s2,
  output s3,
  output s4,
  output s5,
  output carry
);

  wire somadorcompleto_1_carry, somadorcompleto_2_carry, somadorcompleto_3_carry, somadorcompleto_4_carry,
       somadorcompleto_5_carry, xor_1_out, xor_2_out, xor_3_out, xor_4_out, xor_5_out, xor_6_out;

  xor xor_1 (xor_1_out, Chave, B1);
  xor xor_2 (xor_2_out, Chave, B0);
  SomadorCompleto somadorcompleto_1 (.a(A0), .b(xor_2_out), .carry_in(1'b1), .carry(somadorcompleto_1_carry), .s0(s0));
  xor xor_3 (xor_3_out, Chave, B2);
  SomadorCompleto somadorcompleto_2 (
    .a(A1), .b(xor_1_out), .carry_in(somadorcompleto_1_carry), .carry(somadorcompleto_2_carry), .s0(s1));
  SomadorCompleto somadorcompleto_3 (
    .a(A2), .b(xor_3_out), .carry_in(somadorcompleto_2_carry), .carry(somadorcompleto_3_carry), .s0(s2));
  xor xor_4 (xor_4_out, Chave, B3);
  SomadorCompleto somadorcompleto_4 (
    .a(A3), .b(xor_4_out), .carry_in(somadorcompleto_3_carry), .carry(somadorcompleto_4_carry), .s0(s3));
  xor xor_5 (xor_5_out, Chave, B4);
  xor xor_6 (xor_6_out, Chave, Sinal_B);
  SomadorCompleto somadorcompleto_5 (
    .a(A4), .b(xor_5_out), .carry_in(somadorcompleto_4_carry), .carry(somadorcompleto_5_carry), .s0(s4));
  SomadorCompleto somadorcompleto_6 (
    .a(Sinal_A), .b(xor_6_out), .carry_in(somadorcompleto_5_carry), .carry(carry), .s0(s5));

  // Notes on the sheet:
  //   Somador/Subtrator e incremento de 1
endmodule

module Ex04 (
  input  Chave,
  input  B0,
  input  A0,
  input  B1,
  input  A1,
  input  B2,
  input  A2,
  input  B3,
  input  A3,
  input  B4,
  input  A4,
  input  Sinal_B,
  input  Sinal_A,
  output s0,
  output s1,
  output s2,
  output s3,
  output s4,
  output s5,
  output out_20,
  output carry
);

  wire or_1_out, somadorcompleto_1_carry, somadorcompleto_2_carry, somadorcompleto_3_carry,
       somadorcompleto_4_carry, somadorcompleto_5_carry, somadorcompleto_6_carry, xor_1_out, xor_2_out,
       xor_3_out, xor_4_out, xor_5_out, xor_6_out;

  SomadorCompleto somadorcompleto_1 (.a(1'b1), .b(1'b1), .carry_in(1'b1), .carry(somadorcompleto_1_carry), .s0(s0));
  or or_1 (or_1_out, Chave, somadorcompleto_1_carry);
  xor xor_1 (xor_1_out, Chave, B0);
  xor xor_2 (xor_2_out, Chave, B1);
  SomadorCompleto somadorcompleto_2 (
    .a(A0), .b(xor_1_out), .carry_in(or_1_out), .carry(somadorcompleto_2_carry), .s0(s1));
  xor xor_3 (xor_3_out, Chave, B2);
  SomadorCompleto somadorcompleto_3 (
    .a(A1), .b(xor_2_out), .carry_in(somadorcompleto_2_carry), .carry(somadorcompleto_3_carry), .s0(s2));
  SomadorCompleto somadorcompleto_4 (
    .a(A2), .b(xor_3_out), .carry_in(somadorcompleto_3_carry), .carry(somadorcompleto_4_carry), .s0(s3));
  xor xor_4 (xor_4_out, Chave, B3);
  SomadorCompleto somadorcompleto_5 (
    .a(A3), .b(xor_4_out), .carry_in(somadorcompleto_4_carry), .carry(somadorcompleto_5_carry), .s0(s4));
  xor xor_5 (xor_5_out, Chave, B4);
  xor xor_6 (xor_6_out, Chave, Sinal_B);
  SomadorCompleto somadorcompleto_6 (
    .a(A4), .b(xor_5_out), .carry_in(somadorcompleto_5_carry), .carry(somadorcompleto_6_carry), .s0(s5));
  SomadorCompleto somadorcompleto_7 (
    .a(Sinal_A), .b(xor_6_out), .carry_in(somadorcompleto_6_carry), .carry(carry), .s0(out_20));

  // Notes on the sheet:
  //   Soma " -1" = 11
  //   Somador/Subtrator e decremento de 1
endmodule

module Ex05 (
  input  A4,
  input  B4,
  input  A3,
  input  B3,
  input  A2,
  input  B2,
  input  A1,
  input  B1,
  input  A0,
  input  B0,
  input  Sinal_A,
  input  Sinal_B,
  output A_B,
  output A___B,
  output A_B_2
);

  wire maiorque_1_eout, maiorque_1_gout, maiorque_2_eout, maiorque_2_gout, maiorque_3_eout, maiorque_3_gout,
       maiorque_4_eout, maiorque_4_gout, maiorque_5_eout, maiorque_5_gout, not_1_out, not_2_out;

  MaiorQue maiorque_1 (.Gin(1'b0), .Ein(1'b1), .x(A4), .y(B4), .Gout(maiorque_1_gout), .Eout(maiorque_1_eout));
  MaiorQue maiorque_2 (
    .Gin(maiorque_1_gout), .Ein(maiorque_1_eout), .x(A3), .y(B3), .Gout(maiorque_2_gout),
    .Eout(maiorque_2_eout));
  MaiorQue maiorque_3 (
    .Gin(maiorque_2_gout), .Ein(maiorque_2_eout), .x(A2), .y(B2), .Gout(maiorque_3_gout),
    .Eout(maiorque_3_eout));
  MaiorQue maiorque_4 (
    .Gin(maiorque_3_gout), .Ein(maiorque_3_eout), .x(A1), .y(B1), .Gout(maiorque_4_gout),
    .Eout(maiorque_4_eout));
  MaiorQue maiorque_5 (
    .Gin(maiorque_4_gout), .Ein(maiorque_4_eout), .x(A0), .y(B0), .Gout(maiorque_5_gout),
    .Eout(maiorque_5_eout));
  not not_1 (not_1_out, Sinal_A);
  not not_2 (not_2_out, Sinal_B);
  MaiorQue maiorque_6 (
    .Gin(maiorque_5_gout), .Ein(maiorque_5_eout), .x(not_1_out), .y(not_2_out), .Gout(A_B), .Eout(A___B));
  and and_1 (A_B_2, ~A___B, ~A_B);  // AND_Gate

  // Notes on the sheet:
  //   ALU comparador aritimético
  //   Fiquei com dúvida quanto ao sinal. Se o sinal de B for 1 e de A for zero já posso considerar B<A. Mas se eu considerar apenas o valor absoluto, funciona.
endmodule

module Ex01 (
  input  Chave,
  input  B0,
  input  A0,
  input  B1,
  input  A1,
  input  B2,
  input  A2,
  input  B3,
  input  A3,
  input  B4,
  input  A4,
  input  Sinal_B,
  input  Sinal_A,
  output s0,
  output s1,
  output s2,
  output s3,
  output s4,
  output s5,
  output carry
);

  wire somadorcompleto_1_carry, somadorcompleto_2_carry, somadorcompleto_3_carry, somadorcompleto_4_carry,
       somadorcompleto_5_carry, xor_1_out, xor_2_out, xor_3_out, xor_4_out, xor_5_out, xor_6_out;

  xor xor_1 (xor_1_out, Chave, B1);
  xor xor_2 (xor_2_out, Chave, B0);
  SomadorCompleto somadorcompleto_1 (.a(A0), .b(xor_2_out), .carry_in(Chave), .carry(somadorcompleto_1_carry), .s0(s0));
  xor xor_3 (xor_3_out, Chave, B2);
  SomadorCompleto somadorcompleto_2 (
    .a(A2), .b(xor_3_out), .carry_in(somadorcompleto_3_carry), .carry(somadorcompleto_2_carry), .s0(s2));
  SomadorCompleto somadorcompleto_3 (
    .a(A1), .b(xor_1_out), .carry_in(somadorcompleto_1_carry), .carry(somadorcompleto_3_carry), .s0(s1));
  xor xor_4 (xor_4_out, Chave, B3);
  SomadorCompleto somadorcompleto_4 (
    .a(A3), .b(xor_4_out), .carry_in(somadorcompleto_2_carry), .carry(somadorcompleto_4_carry), .s0(s3));
  xor xor_5 (xor_5_out, Chave, Sinal_B);
  xor xor_6 (xor_6_out, Chave, B4);
  SomadorCompleto somadorcompleto_5 (
    .a(A4), .b(xor_6_out), .carry_in(somadorcompleto_4_carry), .carry(somadorcompleto_5_carry), .s0(s4));
  SomadorCompleto somadorcompleto_6 (
    .a(Sinal_A), .b(xor_5_out), .carry_in(somadorcompleto_5_carry), .carry(carry), .s0(s5));
endmodule

// GE
module MaiorQue (
  input  x,
  input  y,
  input  Gin,
  input  Ein,
  output Gout,
  output Eout
);

  wire and_1_out, and_2_out, and_3_out, and_4_out, not_1_out, not_2_out;

  not not_1 (not_1_out, x);
  not not_2 (not_2_out, y);
  and and_1 (and_1_out, y, x, Ein);
  and and_2 (and_2_out, Gin, Ein);
  or or_1 (Gout, Gin, and_3_out);
  and and_3 (and_3_out, not_2_out, x, Ein);
  and and_4 (and_4_out, Ein, not_2_out, not_1_out);
  or or_2 (Eout, and_4_out, and_1_out, and_2_out);
endmodule
