// Logisim project guia05.circ as structural Verilog
// FA
module Full_Adder (
  input  carry_in,
  input  a,
  input  b,
  output s1,
  output s0
);

  wire and_1_out, and_2_out, xor_1_out;

  and and_1 (and_1_out, a, b);
  or or_1 (s1, and_1_out, and_2_out);
  and and_2 (and_2_out, carry_in, xor_1_out);
  xor xor_1 (xor_1_out, a, b);
  xor xor_2 (s0, carry_in, xor_1_out);
endmodule

// HA
module Half_Adder (
  input  a,
  input  b,
  output s1,
  output s0
);

  and and_1 (s1, a, b);
  xor xor_1 (s0, a, b);
endmodule

// HS
module Half_Subtractor (
  input  a,
  input  b,
  output s1,
  output s0
);

  wire not_1_out;

  not not_1 (not_1_out, a);
  and and_1 (s1, not_1_out, b);
  xor xor_1 (s0, a, b);
endmodule

// FS
module Full_Subtractor (
  input  borrow_in,
  input  a,
  input  b,
  output s1,
  output s0
);

  wire and_1_out, and_2_out, not_1_out, not_2_out, xor_1_out;

  not not_1 (not_1_out, a);
  and and_1 (and_1_out, not_1_out, b);
  or or_1 (s1, and_1_out, and_2_out);
  not not_2 (not_2_out, xor_1_out);
  and and_2 (and_2_out, borrow_in, not_2_out);
  xor xor_1 (xor_1_out, a, b);
  xor xor_2 (s0, borrow_in, xor_1_out);
endmodule

// E
module Equals (
  input  a,
  input  b,
  output s
);

  xnor xnor_1 (s, a, b);
endmodule

// D
module Different (
  input  a,
  input  b,
  output s
);

  xor xor_1 (s, a, b);
endmodule

// C1
module Complement_1 (
  input  in_1,
  input  in_2,
  input  in_3,
  input  in_4,
  input  in_5,
  input  in_6,
  output out_7,
  output out_8,
  output out_9,
  output out_10,
  output out_11,
  output out_12
);

  not not_1 (out_8, in_2);
  not not_2 (out_9, in_3);
  not not_3 (out_7, in_1);
  not not_4 (out_10, in_4);
  not not_5 (out_12, in_6);
  not not_6 (out_11, in_5);
endmodule

// AA
module Algebric_Adder (
  input  key,
  input  a,
  input  b,
  output s1,
  output s0
);

  wire and_1_out, and_2_out, or_1_out, xor_3_out, xor_4_out;

  and and_1 (and_1_out, a, xor_3_out);
  and and_2 (and_2_out, key, xor_4_out);
  or or_1 (or_1_out, and_1_out, and_2_out);
  xor xor_1 (s1, key, or_1_out);
  xor xor_2 (s0, key, xor_4_out);
  xor xor_3 (xor_3_out, key, b);
  xor xor_4 (xor_4_out, a, xor_3_out);
endmodule

// +1
module Incremento (
  input  in_1,
  input  in_2,
  input  in_3,
  input  in_4,
  input  in_5,
  input  in_6,
  output out_7,
  output out_8,
  output out_9,
  output out_10,
  output out_11,
  output out_12
);

  wire half_adder_1_s1, half_adder_2_s1, half_adder_3_s1, half_adder_4_s1, half_adder_5_s1, not_1_out,
       xor_2_out;

  xor xor_1 (out_7, in_1, half_adder_1_s1);
  Half_Adder half_adder_1 (.s1(half_adder_1_s1), .s0(out_8), .a(in_2), .b(half_adder_3_s1));
  Half_Adder half_adder_2 (.s1(half_adder_2_s1), .s0(out_10), .a(in_4), .b(half_adder_4_s1));
  Half_Adder half_adder_3 (.s1(half_adder_3_s1), .s0(out_9), .a(in_3), .b(half_adder_2_s1));
  Half_Adder half_adder_4 (.s1(half_adder_4_s1), .s0(out_11), .a(in_5), .b(half_adder_5_s1));
  Half_Adder half_adder_5 (.s1(half_adder_5_s1), .s0(out_12), .a(in_6), .b(xor_2_out));
  xor xor_2 (xor_2_out, in_6, not_1_out);
  not not_1 (not_1_out, in_6);
endmodule

// -1
module Decremento (
  input  in_1,
  input  in_2,
  input  in_3,
  input  in_4,
  input  in_5,
  input  in_6,
  output out_7,
  output out_8,
  output out_9,
  output out_10,
  output out_11,
  output out_12
);

  wire half_subtractor_1_s1, half_subtractor_2_s1, half_subtractor_3_s1, half_subtractor_4_s1,
       half_subtractor_5_s1, not_1_out, xor_2_out;

  xor xor_1 (out_7, in_1, half_subtractor_1_s1);
  Half_Subtractor half_subtractor_1 (.s1(half_subtractor_1_s1), .s0(out_8), .a(in_2), .b(half_subtractor_3_s1));
  Half_Subtractor half_subtractor_2 (.s1(half_subtractor_2_s1), .s0(out_10), .a(in_4), .b(half_subtractor_4_s1));
  Half_Subtractor half_subtractor_3 (.s1(half_subtractor_3_s1), .s0(out_9), .a(in_3), .b(half_subtractor_2_s1));
  Half_Subtractor half_subtractor_4 (.s1(half_subtractor_4_s1), .s0(out_11), .a(in_5), .b(half_subtractor_5_s1));
  Half_Subtractor half_subtractor_5 (.s1(half_subtractor_5_s1), .s0(out_12), .a(in_6), .b(xor_2_out));
  xor xor_2 (xor_2_out, in_6, not_1_out);
  not not_1 (not_1_out, in_6);
endmodule

// L
module Less (
  input  in_1,
  input  in_2,
  input  a,
  input  in_4,
  input  in_5,
  input  in_6,
  input  in_7,
  input  in_8,
  input  b,
  input  in_10,
  input  in_11,
  input  in_12,
  output out_13
);

  wire full_subtractor_1_s1, full_subtractor_2_s1, full_subtractor_3_s1, full_subtractor_4_s1,
       half_subtractor_1_s1, xor_1_out;

  Full_Subtractor full_subtractor_1 (
    .borrow_in(full_subtractor_2_s1), .s1(full_subtractor_1_s1), .a(in_2), .b(in_8));  // open: s0
  xor xor_1 (xor_1_out, in_1, in_7);
  xor xor_2 (out_13, xor_1_out, full_subtractor_1_s1);
  Full_Subtractor full_subtractor_2 (
    .borrow_in(full_subtractor_3_s1), .s1(full_subtractor_2_s1), .a(a), .b(b));  // open: s0
  Full_Subtractor full_subtractor_3 (
    .borrow_in(full_subtractor_4_s1), .s1(full_subtractor_3_s1), .a(in_4), .b(in_10));  // open: s0
  Full_Subtractor full_subtractor_4 (
    .borrow_in(half_subtractor_1_s1), .s1(full_subtractor_4_s1), .a(in_5), .b(in_11));  // open: s0
  Half_Subtractor half_subtractor_1 (.s1(half_subtractor_1_s1), .a(in_6), .b(in_12));  // open: s0
endmodule

// EQ
module Equals_6bits (
  input  in_1,
  input  in_2,
  input  a,
  input  in_4,
  input  in_5,
  input  in_6,
  input  in_7,
  input  in_8,
  input  b,
  input  in_10,
  input  in_11,
  input  in_12,
  output s
);

  wire equals_1_s, equals_2_s, equals_3_s, equals_4_s, equals_5_s, equals_6_s;

  Equals equals_1 (.a(in_1), .b(in_7), .s(equals_1_s));
  Equals equals_2 (.a(a), .b(b), .s(equals_2_s));
  Equals equals_3 (.a(in_2), .b(in_8), .s(equals_3_s));
  Equals equals_4 (.a(in_5), .b(in_11), .s(equals_4_s));
  Equals equals_5 (.a(in_4), .b(in_10), .s(equals_5_s));
  and and_1 (s, equals_1_s, equals_3_s, equals_2_s, equals_5_s, equals_4_s, equals_6_s);
  Equals equals_6 (.a(in_6), .b(in_12), .s(equals_6_s));
endmodule

// G
module Greater (
  input  in_1,
  input  in_2,
  input  a,
  input  in_4,
  input  in_5,
  input  in_6,
  input  in_7,
  input  in_8,
  input  b,
  input  in_10,
  input  in_11,
  input  in_12,
  output out_13
);

  wire equals_6bits_1_s, less_1_out_13;

  Less less_1 (
    .in_1(in_1), .in_2(in_2), .a(a), .in_4(in_4), .in_5(in_5), .in_6(in_6), .in_7(in_7), .in_8(in_8), .b(b),
    .in_10(in_10), .in_11(in_11), .in_12(in_12), .out_13(less_1_out_13));
  nor nor_1 (out_13, less_1_out_13, equals_6bits_1_s);
  Equals_6bits equals_6bits_1 (
    .in_1(in_1), .in_2(in_2), .a(a), .in_4(in_4), .in_5(in_5), .in_6(in_6), .in_7(in_7), .in_8(in_8), .b(b),
    .in_10(in_10), .in_11(in_11), .in_12(in_12), .s(equals_6bits_1_s));
endmodule

// OvrFlw
module Overflow (
  input  s,
  input  a,
  input  b,
  input  key,
  output out_5
);

  wire and_1_out, and_2_out, not_1_out, not_2_out, not_3_out, not_4_out;

  not not_1 (not_1_out, a);
  not not_2 (not_2_out, key);
  not not_3 (not_3_out, b);
  and and_1 (and_1_out, s, not_1_out, not_3_out, not_2_out);
  not not_4 (not_4_out, a);
  and and_2 (and_2_out, not_4_out, b, s, key);
  or or_1 (out_5, and_1_out, and_2_out);
endmodule

// Sinal
module Signal (
  input  in_1,
  input  resultado,
  input  in_3,
  input  in_4,
  input  in_5,
  input  in_6,
  output MINUS,
  output PLUS
);

  wire not_1_out, or_1_out;

  and and_1 (MINUS, in_1, or_1_out);
  or or_1 (or_1_out, in_1, resultado, in_3, in_4, in_5, in_6);
  not not_1 (not_1_out, in_1);
  and and_2 (PLUS, or_1_out, not_1_out);
endmodule

module LU (
  input  in_1,
  input  in_2,
  input  a,
  input  in_4,
  input  in_5,
  input  in_6,
  input  in_7,
  input  in_8,
  input  b,
  input  in_10,
  input  in_11,
  input  in_12,
  output out_13,
  output out_14,
  output out_15
);

  Less less_1 (
    .in_1(in_1), .in_2(in_2), .a(a), .in_4(in_4), .in_5(in_5), .in_6(in_6), .in_7(in_7), .in_8(in_8), .b(b),
    .in_10(in_10), .in_11(in_11), .in_12(in_12), .out_13(out_13));
  Equals_6bits equals_6bits_1 (
    .in_1(in_1), .in_2(in_2), .a(a), .in_4(in_4), .in_5(in_5), .in_6(in_6), .in_7(in_7), .in_8(in_8), .b(b),
    .in_10(in_10), .in_11(in_11), .in_12(in_12), .s(out_14));
  Greater greater_1 (
    .in_1(in_1), .in_2(in_2), .a(a), .in_4(in_4), .in_5(in_5), .in_6(in_6), .in_7(in_7), .in_8(in_8), .b(b),
    .in_10(in_10), .in_11(in_11), .in_12(in_12), .out_13(out_15));
endmodule

// AU
module SomadorAlgebrico1 (
  input  in_1,
  input  in_2,
  input  a,
  input  in_4,
  input  in_5,
  input  in_6,
  input  in_7,
  input  in_8,
  input  b,
  input  in_10,
  input  in_11,
  input  in_12,
  input  key,
  output out_14,
  output out_15,
  output a___1,
  output out_17,
  output out_18,
  output out_19,
  output out_20,
  output out_21,
  output a___1_2,
  output out_23,
  output out_24,
  output out_25,
  output out_26,
  output out_27,
  output out_28,
  output out_29,
  output out_30,
  output out_31,
  output Overflow,
  output Flag__Zero,
  output Carry
);

  wire full_adder_1_s1, full_adder_2_s1, full_adder_3_s1, full_adder_4_s1, full_adder_5_s1, xor_1_out,
       xor_3_out, xor_4_out, xor_5_out, xor_6_out, xor_7_out, xor_8_out;

  Decremento decremento_1 (
    .in_1(in_1), .in_2(in_2), .in_3(a), .in_4(in_4), .in_5(in_5), .in_6(in_6), .out_7(out_14),
    .out_8(out_15), .out_9(a___1), .out_10(out_17), .out_11(out_18), .out_12(out_19));
  Incremento incremento_1 (
    .in_1(in_1), .in_2(in_2), .in_3(a), .in_4(in_4), .in_5(in_5), .in_6(in_6), .out_7(out_20),
    .out_8(out_21), .out_9(a___1_2), .out_10(out_23), .out_11(out_24), .out_12(out_25));
  xor xor_1 (xor_1_out, in_1, xor_3_out);
  xor xor_2 (out_26, xor_1_out, full_adder_1_s1);
  nor nor_1 (Flag__Zero, out_26, out_27, out_28, out_29, out_30, out_31);
  xor xor_3 (xor_3_out, in_7, key);
  Full_Adder full_adder_1 (.carry_in(full_adder_2_s1), .s1(full_adder_1_s1), .s0(out_27), .a(in_2), .b(xor_5_out));
  or or_1 (Carry, full_adder_1_s1, full_adder_2_s1, full_adder_3_s1, full_adder_4_s1, full_adder_5_s1);
  xor xor_4 (xor_4_out, b, key);
  xor xor_5 (xor_5_out, in_8, key);
  Full_Adder full_adder_2 (.carry_in(full_adder_3_s1), .s1(full_adder_2_s1), .s0(out_28), .a(a), .b(xor_4_out));
  xor xor_6 (xor_6_out, in_10, key);
  Full_Adder full_adder_3 (.carry_in(full_adder_4_s1), .s1(full_adder_3_s1), .s0(out_29), .a(in_4), .b(xor_6_out));
  xor xor_7 (xor_7_out, in_11, key);
  Full_Adder full_adder_4 (.carry_in(full_adder_5_s1), .s1(full_adder_4_s1), .s0(out_30), .a(in_5), .b(xor_7_out));
  xor xor_8 (xor_8_out, in_12, key);
  Full_Adder full_adder_5 (.carry_in(key), .s1(full_adder_5_s1), .s0(out_31), .a(in_6), .b(xor_8_out));
  Overflow overflow_1 (.s(out_26), .a(in_1), .b(in_7), .out_5(Overflow), .key(key));

  // Notes on the sheet:
  //   Resultado
  //   0 = Soma
  //   1 = Subtracao
endmodule

// AU
module SomadorAlgebrico2 (
  input  in_1,
  input  in_2,
  input  a,
  input  in_4,
  input  in_5,
  input  in_6,
  input  in_7,
  input  in_8,
  input  b,
  input  in_10,
  input  in_11,
  input  in_12,
  input  key,
  output out_14,
  output out_15,
  output a___1,
  output out_17,
  output out_18,
  output out_19,
  output out_20,
  output out_21,
  output a___1_2,
  output out_23,
  output out_24,
  output out_25,
  output out_26,
  output out_27,
  output out_28,
  output out_29,
  output out_30,
  output out_31,
  output Overflow,
  output Flag__Zero,
  output Carry,
  output N,
  output P
);

  wire full_adder_1_s1, full_adder_2_s1, full_adder_3_s1, full_adder_4_s1, full_adder_5_s1, xor_1_out,
       xor_2_out, xor_4_out, xor_5_out, xor_6_out, xor_7_out, xor_8_out;

  Decremento decremento_1 (
    .in_1(in_1), .in_2(in_2), .in_3(a), .in_4(in_4), .in_5(in_5), .in_6(in_6), .out_7(out_14),
    .out_8(out_15), .out_9(a___1), .out_10(out_17), .out_11(out_18), .out_12(out_19));
  Incremento incremento_1 (
    .in_1(in_1), .in_2(in_2), .in_3(a), .in_4(in_4), .in_5(in_5), .in_6(in_6), .out_7(out_20),
    .out_8(out_21), .out_9(a___1_2), .out_10(out_23), .out_11(out_24), .out_12(out_25));
  xor xor_1 (xor_1_out, in_1, xor_2_out);
  nor nor_1 (Flag__Zero, out_26, out_27, out_28, out_29, out_30, out_31);
  xor xor_2 (xor_2_out, in_7, key);
  Full_Adder full_adder_1 (.carry_in(full_adder_2_s1), .s1(full_adder_1_s1), .s0(out_27), .a(in_2), .b(xor_4_out));
  xor xor_3 (out_26, xor_1_out, full_adder_1_s1);
  or or_1 (Carry, full_adder_1_s1, full_adder_2_s1, full_adder_3_s1, full_adder_4_s1, full_adder_5_s1);
  xor xor_4 (xor_4_out, in_8, key);
  Full_Adder full_adder_2 (.carry_in(full_adder_3_s1), .s1(full_adder_2_s1), .s0(out_28), .a(a), .b(xor_5_out));
  xor xor_5 (xor_5_out, b, key);
  xor xor_6 (xor_6_out, in_10, key);
  Full_Adder full_adder_3 (.carry_in(full_adder_4_s1), .s1(full_adder_3_s1), .s0(out_29), .a(in_4), .b(xor_6_out));
  xor xor_7 (xor_7_out, in_11, key);
  Full_Adder full_adder_4 (.carry_in(full_adder_5_s1), .s1(full_adder_4_s1), .s0(out_30), .a(in_5), .b(xor_7_out));
  Signal signal_1 (
    .in_1(out_26), .resultado(out_27), .in_3(out_28), .in_4(out_29), .in_5(out_30), .in_6(out_31), .MINUS(N),
    .PLUS(P));
  xor xor_8 (xor_8_out, in_12, key);
  Full_Adder full_adder_5 (.carry_in(key), .s1(full_adder_5_s1), .s0(out_31), .a(in_6), .b(xor_8_out));
  Overflow overflow_1 (.s(out_26), .a(in_1), .b(in_7), .out_5(Overflow), .key(key));

  // Notes on the sheet:
  //   Resultado
  //   0 = Soma
  //   1 = Subtracao
endmodule

module Exemplo0031 (
  input  in_1,
  input  a,
  input  in_3,
  input  in_4,
  input  in_5,
  input  in_6,
  input  in_7,
  input  b,
  input  in_9,
  input  in_10,
  input  in_11,
  input  in_12,
  input  key,
  output out_14,
  output out_15,
  output out_16,
  output out_17,
  output out_18,
  output out_19
);

  wire full_adder_1_s1, full_adder_2_s1, full_adder_3_s1, full_adder_4_s1, full_adder_5_s1, xor_1_out,
       xor_2_out, xor_4_out, xor_5_out, xor_6_out, xor_7_out, xor_8_out;

  xor xor_1 (xor_1_out, in_1, xor_2_out);
  xor xor_2 (xor_2_out, in_7, key);
  Full_Adder full_adder_1 (.carry_in(full_adder_2_s1), .s1(full_adder_1_s1), .s0(out_15), .a(a), .b(xor_4_out));
  xor xor_3 (out_14, xor_1_out, full_adder_1_s1);
  xor xor_4 (xor_4_out, b, key);
  Full_Adder full_adder_2 (.carry_in(full_adder_3_s1), .s1(full_adder_2_s1), .s0(out_16), .a(in_3), .b(xor_6_out));
  xor xor_5 (xor_5_out, in_10, key);
  xor xor_6 (xor_6_out, in_9, key);
  Full_Adder full_adder_3 (.carry_in(full_adder_4_s1), .s1(full_adder_3_s1), .s0(out_17), .a(in_4), .b(xor_5_out));
  xor xor_7 (xor_7_out, in_11, key);
  Full_Adder full_adder_4 (.carry_in(full_adder_5_s1), .s1(full_adder_4_s1), .s0(out_18), .a(in_5), .b(xor_7_out));
  xor xor_8 (xor_8_out, in_12, key);
  Full_Adder full_adder_5 (.carry_in(key), .s1(full_adder_5_s1), .s0(out_19), .a(in_6), .b(xor_8_out));

  // Notes on the sheet:
  //   Resultado
  //   0 = Soma
  //   1 = Subtracao
endmodule

module Exemplo0032 (
  input  in_1,
  input  in_2,
  input  a,
  input  in_4,
  input  in_5,
  input  in_6,
  input  in_7,
  input  in_8,
  input  b,
  input  in_10,
  input  in_11,
  input  in_12,
  input  key,
  output out_14,
  output out_15,
  output out_16,
  output out_17,
  output out_18,
  output out_19,
  output Flag__Zero
);

  wire full_adder_1_s1, full_adder_2_s1, full_adder_3_s1, full_adder_4_s1, full_adder_5_s1, xor_1_out,
       xor_2_out, xor_4_out, xor_5_out, xor_6_out, xor_7_out, xor_8_out;

  xor xor_1 (xor_1_out, in_1, xor_2_out);
  nor nor_1 (Flag__Zero, out_14, out_15, out_16, out_17, out_18, out_19);
  xor xor_2 (xor_2_out, in_7, key);
  Full_Adder full_adder_1 (.carry_in(full_adder_2_s1), .s1(full_adder_1_s1), .s0(out_15), .a(in_2), .b(xor_4_out));
  xor xor_3 (out_14, xor_1_out, full_adder_1_s1);
  xor xor_4 (xor_4_out, in_8, key);
  Full_Adder full_adder_2 (.carry_in(full_adder_3_s1), .s1(full_adder_2_s1), .s0(out_16), .a(a), .b(xor_6_out));
  xor xor_5 (xor_5_out, in_10, key);
  xor xor_6 (xor_6_out, b, key);
  Full_Adder full_adder_3 (.carry_in(full_adder_4_s1), .s1(full_adder_3_s1), .s0(out_17), .a(in_4), .b(xor_5_out));
  xor xor_7 (xor_7_out, in_11, key);
  Full_Adder full_adder_4 (.carry_in(full_adder_5_s1), .s1(full_adder_4_s1), .s0(out_18), .a(in_5), .b(xor_7_out));
  xor xor_8 (xor_8_out, in_12, key);
  Full_Adder full_adder_5 (.carry_in(key), .s1(full_adder_5_s1), .s0(out_19), .a(in_6), .b(xor_8_out));

  // Notes on the sheet:
  //   Resultado
  //   0 = Soma
  //   1 = Subtracao
endmodule

module Exemplo0033 (
  input  in_1,
  input  in_2,
  input  a,
  input  in_4,
  input  in_5,
  input  in_6,
  input  in_7,
  input  in_8,
  input  b,
  input  in_10,
  input  in_11,
  input  in_12,
  input  key,
  output out_14,
  output out_15,
  output a___1,
  output out_17,
  output out_18,
  output out_19,
  output out_20,
  output out_21,
  output Resultado,
  output out_23,
  output out_24,
  output out_25,
  output Flag__Zero
);

  wire full_adder_1_s1, full_adder_2_s1, full_adder_3_s1, full_adder_4_s1, full_adder_5_s1, xor_1_out,
       xor_2_out, xor_4_out, xor_5_out, xor_6_out, xor_7_out, xor_8_out;

  Incremento incremento_1 (
    .in_1(in_1), .in_2(in_2), .in_3(a), .in_4(in_4), .in_5(in_5), .in_6(in_6), .out_7(out_14),
    .out_8(out_15), .out_9(a___1), .out_10(out_17), .out_11(out_18), .out_12(out_19));
  xor xor_1 (xor_1_out, in_1, xor_2_out);
  nor nor_1 (Flag__Zero, out_20, out_21, Resultado, out_23, out_24, out_25);
  xor xor_2 (xor_2_out, in_7, key);
  Full_Adder full_adder_1 (.carry_in(full_adder_2_s1), .s1(full_adder_1_s1), .s0(out_21), .a(in_2), .b(xor_4_out));
  xor xor_3 (out_20, xor_1_out, full_adder_1_s1);
  xor xor_4 (xor_4_out, in_8, key);
  Full_Adder full_adder_2 (.carry_in(full_adder_3_s1), .s1(full_adder_2_s1), .s0(Resultado), .a(a), .b(xor_6_out));
  xor xor_5 (xor_5_out, in_10, key);
  xor xor_6 (xor_6_out, b, key);
  Full_Adder full_adder_3 (.carry_in(full_adder_4_s1), .s1(full_adder_3_s1), .s0(out_23), .a(in_4), .b(xor_5_out));
  xor xor_7 (xor_7_out, in_11, key);
  Full_Adder full_adder_4 (.carry_in(full_adder_5_s1), .s1(full_adder_4_s1), .s0(out_24), .a(in_5), .b(xor_7_out));
  xor xor_8 (xor_8_out, in_12, key);
  Full_Adder full_adder_5 (.carry_in(key), .s1(full_adder_5_s1), .s0(out_25), .a(in_6), .b(xor_8_out));

  // Notes on the sheet:
  //   0 = Soma
  //   1 = Subtracao
endmodule

// AU
module Exemplo0034 (
  input  in_1,
  input  in_2,
  input  a,
  input  in_4,
  input  in_5,
  input  in_6,
  input  in_7,
  input  in_8,
  input  b,
  input  in_10,
  input  in_11,
  input  in_12,
  input  key,
  output out_14,
  output out_15,
  output a___1,
  output out_17,
  output out_18,
  output out_19,
  output out_20,
  output out_21,
  output a___1_2,
  output out_23,
  output out_24,
  output out_25,
  output out_26,
  output out_27,
  output out_28,
  output Resultado,
  output out_30,
  output out_31,
  output Flag__Zero
);

  wire full_adder_1_s1, full_adder_2_s1, full_adder_3_s1, full_adder_4_s1, full_adder_5_s1, xor_1_out,
       xor_2_out, xor_4_out, xor_5_out, xor_6_out, xor_7_out, xor_8_out;

  Decremento decremento_1 (
    .in_1(in_1), .in_2(in_2), .in_3(a), .in_4(in_4), .in_5(in_5), .in_6(in_6), .out_7(out_14),
    .out_8(out_15), .out_9(a___1), .out_10(out_17), .out_11(out_18), .out_12(out_19));
  Incremento incremento_1 (
    .in_1(in_1), .in_2(in_2), .in_3(a), .in_4(in_4), .in_5(in_5), .in_6(in_6), .out_7(out_20),
    .out_8(out_21), .out_9(a___1_2), .out_10(out_23), .out_11(out_24), .out_12(out_25));
  nor nor_1 (Flag__Zero, out_26, out_27, out_28, Resultado, out_30, out_31);
  xor xor_1 (xor_1_out, in_7, key);
  xor xor_2 (xor_2_out, in_1, xor_1_out);
  xor xor_3 (out_26, xor_2_out, full_adder_1_s1);
  xor xor_4 (xor_4_out, in_8, key);
  Full_Adder full_adder_1 (.carry_in(full_adder_2_s1), .s1(full_adder_1_s1), .s0(out_27), .a(in_2), .b(xor_4_out));
  xor xor_5 (xor_5_out, b, key);
  Full_Adder full_adder_2 (.carry_in(full_adder_3_s1), .s1(full_adder_2_s1), .s0(out_28), .a(a), .b(xor_5_out));
  xor xor_6 (xor_6_out, in_10, key);
  Full_Adder full_adder_3 (.carry_in(full_adder_5_s1), .s1(full_adder_3_s1), .s0(Resultado), .a(in_4), .b(xor_6_out));
  xor xor_7 (xor_7_out, in_11, key);
  Full_Adder full_adder_4 (.carry_in(key), .s1(full_adder_4_s1), .s0(out_31), .a(in_6), .b(xor_8_out));
  Full_Adder full_adder_5 (.carry_in(full_adder_4_s1), .s1(full_adder_5_s1), .s0(out_30), .a(in_5), .b(xor_7_out));
  xor xor_8 (xor_8_out, in_12, key);

  // Notes on the sheet:
  //   0 = Soma
  //   1 = Subtracao
endmodule

module Exemplo0035 (
  input  in_1,
  input  in_2,
  input  a,
  input  in_4,
  input  in_5,
  input  in_6,
  input  in_7,
  input  in_8,
  input  b,
  input  in_10,
  input  in_11,
  input  in_12,
  input  key,
  output L,
  output E,
  output G,
  output out_17,
  output out_18,
  output out_19,
  output out_20,
  output out_21,
  output out_22,
  output out_23,
  output out_24,
  output out_25,
  output out_26,
  output out_27,
  output out_28,
  output Flag__Zero,
  output out_30,
  output out_31,
  output out_32,
  output Resultado,
  output out_34,
  output out_35
);

  LU lu_1 (
    .in_1(in_1), .in_2(in_2), .a(a), .in_4(in_4), .in_5(in_5), .in_6(in_6), .in_7(in_7), .in_8(in_8), .b(b),
    .in_10(in_10), .in_11(in_11), .in_12(in_12), .out_13(L), .out_14(E), .out_15(G));
  Exemplo0034 exemplo0034_1 (
    .in_1(in_1), .in_2(in_2), .a(a), .in_4(in_4), .in_5(in_5), .in_6(in_6), .in_7(in_7), .in_8(in_8), .b(b),
    .in_10(in_10), .in_11(in_11), .in_12(in_12), .out_14(out_17), .out_15(out_18), .a___1(out_19),
    .out_17(out_20), .out_18(out_21), .out_19(out_22), .out_20(out_23), .out_21(out_24), .a___1_2(out_25),
    .out_23(out_26), .out_24(out_27), .out_25(out_28), .Flag__Zero(Flag__Zero), .out_26(out_30),
    .out_27(out_31), .out_28(out_32), .Resultado(Resultado), .out_30(out_34), .out_31(out_35), .key(key));

  // Notes on the sheet:
  //   a - 1
  //   a + 1
  //   0 = Soma
  //   1 = Subtracao
endmodule

module Exemplo0036 (
  input  in_1,
  input  in_2,
  input  in_3,
  input  in_4,
  input  in_5,
  input  in_6,
  input  in_7,
  input  in_8,
  input  in_9,
  input  in_10,
  input  in_11,
  input  in_12,
  input  key,
  output L,
  output E,
  output G,
  output out_17,
  output out_18,
  output out_19,
  output out_20,
  output out_21,
  output out_22,
  output out_23,
  output out_24,
  output out_25,
  output out_26,
  output out_27,
  output out_28,
  output Flag__Zero,
  output Carry,
  output Overflow,
  output out_32,
  output out_33,
  output out_34,
  output Resultado,
  output out_36,
  output out_37
);

  LU lu_1 (
    .in_1(in_1), .in_2(in_2), .a(in_3), .in_4(in_4), .in_5(in_5), .in_6(in_6), .in_7(in_7), .in_8(in_8),
    .b(in_9), .in_10(in_10), .in_11(in_11), .in_12(in_12), .out_13(L), .out_14(E), .out_15(G));
  SomadorAlgebrico1 somadoralgebrico1_1 (
    .in_1(in_1), .in_2(in_2), .a(in_3), .in_4(in_4), .in_5(in_5), .in_6(in_6), .in_7(in_7), .in_8(in_8),
    .b(in_9), .in_10(in_10), .in_11(in_11), .in_12(in_12), .out_14(out_17), .out_15(out_18), .a___1(out_19),
    .out_17(out_20), .out_18(out_21), .out_19(out_22), .out_20(out_23), .out_21(out_24), .a___1_2(out_25),
    .out_23(out_26), .out_24(out_27), .out_25(out_28), .Flag__Zero(Flag__Zero), .Carry(Carry),
    .out_26(out_32), .out_27(out_33), .out_28(out_34), .out_29(Resultado), .out_30(out_36), .out_31(out_37),
    .Overflow(Overflow), .key(key));

  // Notes on the sheet:
  //   a - 1
  //   a + 1
  //   0 = Soma
  //   1 = Subtracao
endmodule

module Exemplo0037 (
  input  in_1,
  input  in_2,
  input  in_3,
  input  in_4,
  input  in_5,
  input  in_6,
  input  in_7,
  input  in_8,
  input  in_9,
  input  in_10,
  input  in_11,
  input  in_12,
  input  key,
  output L,
  output E,
  output G,
  output out_17,
  output out_18,
  output out_19,
  output out_20,
  output out_21,
  output out_22,
  output out_23,
  output out_24,
  output out_25,
  output out_26,
  output out_27,
  output out_28,
  output Flag__Zero,
  output Carry,
  output Overflow,
  output N,
  output P,
  output out_34,
  output out_35,
  output out_36,
  output Resultado,
  output out_38,
  output out_39
);

  LU lu_1 (
    .in_1(in_1), .in_2(in_2), .a(in_3), .in_4(in_4), .in_5(in_5), .in_6(in_6), .in_7(in_7), .in_8(in_8),
    .b(in_9), .in_10(in_10), .in_11(in_11), .in_12(in_12), .out_13(L), .out_14(E), .out_15(G));
  SomadorAlgebrico2 somadoralgebrico2_1 (
    .in_1(in_1), .in_2(in_2), .a(in_3), .in_4(in_4), .in_5(in_5), .in_6(in_6), .in_7(in_7), .in_8(in_8),
    .b(in_9), .in_10(in_10), .in_11(in_11), .in_12(in_12), .out_14(out_17), .out_15(out_18), .a___1(out_19),
    .out_17(out_20), .out_18(out_21), .out_19(out_22), .out_20(out_23), .out_21(out_24), .a___1_2(out_25),
    .out_23(out_26), .out_24(out_27), .out_25(out_28), .Flag__Zero(Flag__Zero), .Carry(Carry),
    .out_26(out_34), .out_27(out_35), .out_28(out_36), .out_29(Resultado), .out_30(out_38), .out_31(out_39),
    .N(N), .P(P), .Overflow(Overflow), .key(key));

  // Notes on the sheet:
  //   a - 1
  //   a + 1
  //   0 = Soma
  //   1 = Subtracao
endmodule
