// Logisim project Exemplo0034.circ as structural Verilog: 1 circuit, main circuit main
module main (
  input  [5:0] x,
  input  [5:0] y,
  output [5:0] s0,
  output [5:0] s2
);

  wire [5:0] and_1_out, and_2_out, or_1_out, or_2_out, undriven, xor_1_out;

  assign y = ~y;  // NOT_Gate not_1, 6 bits wide
  assign or_1_out = y | x;  // OR_Gate or_1, 6 bits wide
  assign and_1_out = x & y;  // AND_Gate and_1, 6 bits wide
  assign or_1_out = ~or_1_out;  // NOT_Gate not_2, 6 bits wide
  assign xor_1_out = undriven ^ or_1_out;  // XOR_Gate xor_1, 6 bits wide
  assign and_2_out = or_1_out & undriven;  // AND_Gate and_2, 6 bits wide
  assign or_2_out = and_2_out | and_1_out;  // OR_Gate or_2, 6 bits wide
  assign s0 = xor_1_out ^ or_2_out;  // XOR_Gate xor_2, 6 bits wide
  assign s2 = xor_1_out & or_2_out;  // AND_Gate and_3, 6 bits wide

  // Notes on the sheet:
  //   Vai Um
endmodule
