// Logisim project Guia05.circ as structural Verilog: 4 circuits, main circuit main
module main (
  input  carry_in_a,
  input  carry_in_b,
  input  a4,
  input  b4,
  input  a3,
  input  b3,
  input  a2,
  input  b2,
  input  a1,
  input  b1,
  input  a0,
  input  b0,
  output carry_out,
  output s4,
  output s3,
  output s2,
  output s1,
  output s0
);

  wire adder_2_cout, adder_3_cout, adder_4_cout, adder_5_cout, or_1_out, xor_1_out, xor_2_out, xor_3_out,
       xor_4_out, xor_5_out;

  or or_1 (or_1_out, carry_in_a, carry_in_b);
  xor xor_1 (xor_1_out, b4, or_1_out);
  xor xor_2 (xor_2_out, b3, or_1_out);
  xor xor_3 (xor_3_out, b2, or_1_out);
  xor xor_4 (xor_4_out, b1, or_1_out);
  xor xor_5 (xor_5_out, b0, or_1_out);
  Adder #(.width(1)) adder_1 (.a(a4), .b(xor_1_out), .out(s4), .cin(adder_2_cout), .cout(carry_out));
  Adder #(.width(1)) adder_2 (.a(a3), .b(xor_2_out), .out(s3), .cin(adder_3_cout), .cout(adder_2_cout));
  Adder #(.width(1)) adder_3 (.a(a2), .b(xor_3_out), .out(s2), .cin(adder_4_cout), .cout(adder_3_cout));
  Adder #(.width(1)) adder_4 (.a(a1), .b(xor_4_out), .out(s1), .cin(adder_5_cout), .cout(adder_4_cout));
  Adder #(.width(1)) adder_5 (.a(a0), .b(xor_5_out), .out(s0), .cin(or_1_out), .cout(adder_5_cout));
endmodule

module _0501 (
  input  carry_in_a,
  input  carry_in_b,
  input  a4,
  input  b4,
  input  a3,
  input  b3,
  input  a2,
  input  b2,
  input  a1,
  input  b1,
  input  a0,
  input  b0,
  output carry_out,
  output s4,
  output s3,
  output s2,
  output s1,
  output s0
);

  wire adder_2_cout, adder_3_cout, adder_4_cout, adder_5_cout, or_1_out, xor_1_out, xor_2_out, xor_3_out,
       xor_4_out, xor_5_out;

  or or_1 (or_1_out, carry_in_a, carry_in_b);
  xor xor_1 (xor_1_out, b4, or_1_out);
  xor xor_2 (xor_2_out, b3, or_1_out);
  xor xor_3 (xor_3_out, b2, or_1_out);
  xor xor_4 (xor_4_out, b1, or_1_out);
  xor xor_5 (xor_5_out, b0, or_1_out);
  Adder #(.width(1)) adder_1 (.a(a4), .b(xor_1_out), .out(s4), .cin(adder_2_cout), .cout(carry_out));
  Adder #(.width(1)) adder_2 (.a(a3), .b(xor_2_out), .out(s3), .cin(adder_3_cout), .cout(adder_2_cout));
  Adder #(.width(1)) adder_3 (.a(a2), .b(xor_3_out), .out(s2), .cin(adder_4_cout), .cout(adder_3_cout));
  Adder #(.width(1)) adder_4 (.a(a1), .b(xor_4_out), .out(s1), .cin(adder_5_cout), .cout(adder_4_cout));
  Adder #(.width(1)) adder_5 (.a(a0), .b(xor_5_out), .out(s0), .cin(or_1_out), .cout(adder_5_cout));
endmodule

module _0502 (
  input  carry_in_a,
  input  carry_in_b,
  input  a4,
  input  b4,
  input  a3,
  input  b3,
  input  a2,
  input  b2,
  input  a1,
  input  b1,
  input  a0,
  input  b0,
  output carry_out,
  output s4,
  output s3,
  output s2,
  output equals_0,
  output s1,
  output s0
);

  wire adder_2_cout, adder_3_cout, adder_4_cout, adder_5_cout, or_1_out, xnor_1_out, xnor_2_out, xnor_3_out,
       xnor_4_out, xnor_5_out, xor_1_out, xor_2_out, xor_3_out, xor_4_out, xor_5_out;

  or or_1 (or_1_out, carry_in_a, carry_in_b);
  xor xor_1 (xor_1_out, b4, or_1_out);
  xor xor_2 (xor_2_out, b3, or_1_out);
  xor xor_3 (xor_3_out, b2, or_1_out);
  xor xor_4 (xor_4_out, b1, or_1_out);
  xor xor_5 (xor_5_out, b0, or_1_out);
  Adder #(.width(1)) adder_1 (.a(a4), .b(xor_1_out), .out(s4), .cin(adder_2_cout), .cout(carry_out));
  Adder #(.width(1)) adder_2 (.a(a3), .b(xor_2_out), .out(s3), .cin(adder_3_cout), .cout(adder_2_cout));
  Adder #(.width(1)) adder_3 (.a(a2), .b(xor_3_out), .out(s2), .cin(adder_4_cout), .cout(adder_3_cout));
  Adder #(.width(1)) adder_4 (.a(a1), .b(xor_4_out), .out(s1), .cin(adder_5_cout), .cout(adder_4_cout));
  Adder #(.width(1)) adder_5 (.a(a0), .b(xor_5_out), .out(s0), .cin(or_1_out), .cout(adder_5_cout));
  xnor xnor_1 (xnor_1_out, s4, 1'b0);
  xnor xnor_2 (xnor_2_out, s3, 1'b0);
  xnor xnor_3 (xnor_3_out, s2, 1'b0);
  xnor xnor_4 (xnor_4_out, s1, 1'b0);
  xnor xnor_5 (xnor_5_out, s0, 1'b0);
  and and_1 (equals_0, xnor_1_out, xnor_2_out, xnor_3_out, xnor_4_out, xnor_5_out);
endmodule

module _0505 (
  input  a0,
  input  b0,
  input  a1,
  input  b1,
  input  a2,
  input  b2,
  input  a3,
  input  b3,
  input  a4,
  input  b4,
  input  a5,
  input  b5,
  output less_than__a___b,
  output equals__a__b,
  output greater_than__a___b
);

  wire and_1_out, and_2_out, and_3_out, and_4_out, and_5_out, and_6_out, and_7_out, and_8_out, and_9_out,
       and_10_out, and_11_out, and_12_out, nor_1_out, nor_2_out, nor_3_out, nor_4_out, nor_5_out, nor_6_out,
       not_1_out, not_2_out, not_3_out, not_4_out, not_5_out, not_6_out, not_7_out, not_8_out, not_9_out,
       not_10_out, not_11_out, not_12_out;

  not not_1 (not_1_out, a0);
  not not_2 (not_2_out, b0);
  not not_3 (not_3_out, a1);
  not not_4 (not_4_out, b1);
  not not_5 (not_5_out, a2);
  not not_6 (not_6_out, b2);
  not not_7 (not_7_out, a3);
  not not_8 (not_8_out, b3);
  not not_9 (not_9_out, a4);
  not not_10 (not_10_out, b4);
  not not_11 (not_11_out, a5);
  not not_12 (not_12_out, b5);
  and and_1 (and_1_out, not_1_out, b0);
  and and_2 (and_2_out, a0, not_2_out);
  and and_3 (and_3_out, not_3_out, b1);
  and and_4 (and_4_out, a1, not_4_out);
  and and_5 (and_5_out, not_5_out, b2);
  and and_6 (and_6_out, a2, not_6_out);
  and and_7 (and_7_out, not_7_out, b3);
  and and_8 (and_8_out, a3, not_8_out);
  and and_9 (and_9_out, not_9_out, b4);
  and and_10 (and_10_out, a4, not_10_out);
  and and_11 (and_11_out, not_11_out, b5);
  and and_12 (and_12_out, a5, not_12_out);
  nor nor_1 (nor_1_out, and_1_out, and_2_out);
  nor nor_2 (nor_2_out, and_3_out, and_4_out);
  nor nor_3 (nor_3_out, and_5_out, and_6_out);
  nor nor_4 (nor_4_out, and_7_out, and_8_out);
  nor nor_5 (nor_5_out, and_9_out, and_10_out);
  nor nor_6 (nor_6_out, and_11_out, and_12_out);
  or or_1 (less_than__a___b, and_1_out, and_3_out, and_5_out, and_7_out, and_9_out, and_11_out);
  and and_13 (equals__a__b, nor_1_out, nor_2_out, nor_3_out, nor_4_out, nor_5_out, nor_6_out);
  or or_2 (greater_than__a___b, and_2_out, and_4_out, and_6_out, and_8_out, and_10_out, and_12_out);
endmodule
