// Logisim project Mealy101.circ as structural Verilog: 1 circuit, main circuit main
module main (
  input  DATA,
  input  RST,
  output out_3
);

  wire CLK_out, d_ff_1_q, d_ff_2_q, d_ff_3_q, not_1_out;

  Clock CLK (.out(CLK_out));
  D_Flip_Flop d_ff_1 (.clk(CLK_out), .D(DATA), .Q(d_ff_1_q), .reset(RST));  // open: Qn, preset, en
  D_Flip_Flop d_ff_2 (.clk(CLK_out), .D(d_ff_1_q), .Q(d_ff_2_q), .reset(RST));  // open: Qn, preset, en
  D_Flip_Flop d_ff_3 (.clk(CLK_out), .D(d_ff_2_q), .Q(d_ff_3_q), .reset(RST));  // open: Qn, preset, en
  and and_1 (out_3, d_ff_3_q, not_1_out, d_ff_1_q);
  not not_1 (not_1_out, d_ff_2_q);

  // Notes on the sheet:
  //   Mealy101
endmodule
