// Logisim project Exemplo0054.circ as structural Verilog: 1 circuit, main circuit main
module main (
  input  Entrada,
  input  Reset,
  output out_3
);

  wire Clk_out, d_ff_1_q, d_ff_2_q, d_ff_3_q, d_ff_4_q, not_1_out;

  Clock Clk (.out(Clk_out));
  D_Flip_Flop d_ff_1 (.clk(Clk_out), .D(Entrada), .Q(d_ff_1_q), .reset(Reset));  // open: Qn, preset, en
  D_Flip_Flop d_ff_2 (.clk(Clk_out), .D(d_ff_1_q), .Q(d_ff_2_q), .reset(Reset));  // open: Qn, preset, en
  D_Flip_Flop d_ff_3 (.clk(Clk_out), .D(d_ff_2_q), .Q(d_ff_3_q), .reset(Reset));  // open: Qn, preset, en
  D_Flip_Flop d_ff_4 (.clk(Clk_out), .D(d_ff_3_q), .Q(d_ff_4_q), .reset(Reset));  // open: Qn, preset, en
  not not_1 (not_1_out, d_ff_4_q);
  and and_1 (out_3, not_1_out, d_ff_3_q, d_ff_2_q, d_ff_1_q);
endmodule
