// Logisim project Exercicio0053.circ as structural Verilog: 1 circuit, main circuit main
module main (
  input  in_1,
  input  in_2,
  output out_3
);

  wire A_q, and_1_out, B_q, C_q, clock_1_out, D_q, not_1_out;

  Clock clock_1 (.out(clock_1_out));
  D_Flip_Flop A (.clk(clock_1_out), .D(in_1), .Q(A_q), .reset(in_2));  // open: Qn, preset, en
  D_Flip_Flop B (.clk(clock_1_out), .D(A_q), .Q(B_q), .reset(in_2));  // open: Qn, preset, en
  D_Flip_Flop C (.clk(clock_1_out), .D(B_q), .Q(C_q), .reset(in_2));  // open: Qn, preset, en
  and and_1 (and_1_out, D_q, C_q, not_1_out, A_q);
  not not_1 (not_1_out, B_q);
  D_Flip_Flop D (.clk(clock_1_out), .D(C_q), .Q(D_q), .reset(in_2));  // open: Qn, preset, en
  D_Flip_Flop d_ff_1 (.clk(clock_1_out), .D(and_1_out), .Q(out_3), .reset(in_2));  // open: Qn, preset, en
endmodule
