// Logisim project Exemplo0054.circ as structural Verilog: 1 circuit, main circuit main
module main (
  input  in_1,
  input  in_2,
  output out_3
);

  wire clock_1_out, d_ff_1_qn, d_ff_2_qn, d_ff_3_q, d_ff_4_q, not_1_out;

  Clock clock_1 (.out(clock_1_out));
  D_Flip_Flop d_ff_1 (.clk(clock_1_out), .D(in_1), .Qn(d_ff_1_qn), .en(in_2));  // open: Q, preset, reset
  D_Flip_Flop d_ff_2 (.clk(clock_1_out), .D(d_ff_1_qn), .Qn(d_ff_2_qn), .en(in_2));  // open: Q, preset, reset
  D_Flip_Flop d_ff_3 (.clk(clock_1_out), .D(d_ff_2_qn), .Q(d_ff_3_q), .en(in_2));  // open: Qn, preset, reset
  not not_1 (not_1_out, d_ff_2_qn);
  D_Flip_Flop d_ff_4 (.clk(clock_1_out), .D(d_ff_3_q), .Q(d_ff_4_q), .reset(in_2));  // open: Qn, preset, en
  and and_1 (out_3, d_ff_3_q, d_ff_4_q, not_1_out, d_ff_1_qn);
endmodule
