// Logisim project exemplo0052.circ as structural Verilog: 1 circuit, main circuit main
module main (
  input  Clock,
  input  in_2,
  input  Reset,
  output out_4
);

  wire d_ff_1_q, d_ff_2_q, d_ff_3_q, not_1_out;

  D_Flip_Flop d_ff_1 (.clk(Clock), .D(in_2), .Q(d_ff_1_q), .reset(Reset));  // open: Qn, preset, en
  D_Flip_Flop d_ff_2 (.clk(Clock), .D(d_ff_1_q), .Q(d_ff_2_q), .reset(Reset));  // open: Qn, preset, en
  not not_1 (not_1_out, d_ff_2_q);
  D_Flip_Flop d_ff_3 (.clk(Clock), .D(d_ff_2_q), .Q(d_ff_3_q), .reset(Reset));  // open: Qn, preset, en
  and and_1 (out_4, d_ff_3_q, not_1_out, d_ff_1_q);
endmodule
