// Logisim project Circuitos.circ as structural Verilog: 1 circuit, main circuit main
module main (
  input  data,
  input  reset,
  input  in_3,
  input  reset_2,
  input  reset_3,
  input  ld,
  input  in_7,
  input  in_8,
  input  in_9,
  input  in_10,
  output out_11,
  output out_12,
  output out_13,
  output out_14,
  output out_15,
  output out_16
);

  wire and_1_out, and_2_out, and_3_out, and_4_out, and_6_out, b_2_q, b_q, clock_1_out, clock_2_out,
       clock_3_out, d_ff_1_q, d_ff_2_q, d_ff_4_q, d_ff_5_q, d_ff_5_qn, d_ff_7_q, d_ff_8_q, not_1_out,
       undriven;

  Clock clock_1 (.out(clock_1_out));
  Clock clock_2 (.out(clock_2_out));
  Clock clock_3 (.out(clock_3_out));
  D_Flip_Flop d_ff_1 (.clk(clock_1_out), .D(data), .Q(d_ff_1_q), .en(reset));  // open: Qn, preset, reset
  D_Flip_Flop d_ff_2 (.clk(clock_2_out), .D(in_3), .Q(d_ff_2_q), .en(reset_2));  // open: Qn, preset, reset
  D_Flip_Flop d_ff_3 (
    .clk(clock_3_out), .D(undriven), .Q(out_13), .preset(and_1_out), .en(reset_3));  // open: Qn, reset
  and and_1 (and_1_out, in_8, ld);
  D_Flip_Flop d_ff_4 (.clk(clock_1_out), .D(d_ff_1_q), .Q(d_ff_4_q), .en(reset));  // open: Qn, preset, reset
  D_Flip_Flop d_ff_5 (
    .clk(clock_2_out), .D(d_ff_2_q), .Q(d_ff_5_q), .Qn(d_ff_5_qn), .en(reset_2));  // open: preset, reset
  D_Flip_Flop d_ff_6 (.clk(clock_3_out), .D(out_13), .Q(out_14), .preset(and_2_out), .en(reset_3));  // open: Qn, reset
  and and_2 (and_2_out, ld, in_9);
  D_Flip_Flop b (.clk(clock_1_out), .D(d_ff_4_q), .Q(b_q), .en(reset));  // open: Qn, preset, reset
  D_Flip_Flop b_2 (.clk(clock_2_out), .D(d_ff_5_q), .Q(b_2_q), .en(reset_2));  // open: Qn, preset, reset
  D_Flip_Flop b_3 (.clk(clock_3_out), .D(out_14), .Q(out_15), .preset(and_3_out), .en(reset_3));  // open: Qn, reset
  and and_3 (and_3_out, ld, in_10);
  D_Flip_Flop d_ff_7 (.clk(clock_1_out), .D(b_q), .Q(d_ff_7_q), .en(reset));  // open: Qn, preset, reset
  D_Flip_Flop d_ff_8 (.clk(clock_2_out), .D(b_2_q), .Q(d_ff_8_q), .reset(reset_2));  // open: Qn, preset, en
  D_Flip_Flop d_ff_9 (.clk(clock_3_out), .D(out_15), .Q(out_16), .preset(and_4_out), .en(reset_3));  // open: Qn, reset
  and and_4 (and_4_out, ld, in_7);
  not not_1 (not_1_out, d_ff_4_q);
  and and_5 (out_11, d_ff_7_q, b_q, not_1_out, d_ff_1_q);
  D_Flip_Flop d_ff_10 (.clk(clock_2_out), .D(and_6_out), .Q(out_12), .reset(reset_2));  // open: Qn, preset, en
  and and_6 (and_6_out, d_ff_8_q, d_ff_5_qn, d_ff_2_q);

  // Notes on the sheet:
  //   clock
  //   clock
  //   clock
  //   d
  //   d
  //   d
  //   Lab 07
  //   c
  //   c
  //   c
  //   a
  //   a
  //   a
  //   Lorena Danielle Gonçalves Bento - 435049
endmodule
