// Logisim project Exemplos_Circuitos.circ as structural Verilog: 3 circuits, main circuit Exemplo0072
module Exemplo0072 (
  input  X,
  input  RESET,
  output S
);

  wire clock_1_out, d_ff_1_q, d_ff_2_q, d_ff_3_q, not_1_out;

  Clock clock_1 (.out(clock_1_out));
  D_Flip_Flop d_ff_1 (.clk(clock_1_out), .D(X), .Q(d_ff_1_q), .reset(RESET));  // open: Qn, preset, en
  D_Flip_Flop d_ff_2 (.clk(clock_1_out), .D(d_ff_1_q), .Q(d_ff_2_q), .reset(RESET));  // open: Qn, preset, en
  D_Flip_Flop d_ff_3 (.clk(clock_1_out), .D(d_ff_2_q), .Q(d_ff_3_q), .reset(RESET));  // open: Qn, preset, en
  not not_1 (not_1_out, d_ff_2_q);
  and and_1 (S, d_ff_3_q, not_1_out, d_ff_1_q);

  // Notes on the sheet:
  //   CLOCK
  //   Mateus Augusto Moraes Ferreira   Matricula:435669
endmodule

module Exemplo0073 (
  input  in_1,
  input  RESET,
  output S
);

  wire CLOCK_out, d_ff_1_q, d_ff_2_q, d_ff_3_q, d_ff_4_q, not_1_out, not_2_out;

  Clock CLOCK (.out(CLOCK_out));
  D_Flip_Flop d_ff_1 (.clk(CLOCK_out), .D(in_1), .Q(d_ff_1_q), .reset(RESET));  // open: Qn, preset, en
  D_Flip_Flop d_ff_2 (.clk(CLOCK_out), .D(d_ff_1_q), .Q(d_ff_2_q), .reset(RESET));  // open: Qn, preset, en
  D_Flip_Flop d_ff_3 (.clk(CLOCK_out), .D(d_ff_2_q), .Q(d_ff_3_q), .reset(RESET));  // open: Qn, preset, en
  D_Flip_Flop d_ff_4 (.clk(CLOCK_out), .D(d_ff_3_q), .Q(d_ff_4_q), .reset(RESET));  // open: Qn, preset, en
  not not_1 (not_1_out, d_ff_4_q);
  not not_2 (not_2_out, d_ff_2_q);
  and and_1 (S, not_1_out, d_ff_3_q, not_2_out, d_ff_1_q);

  // Notes on the sheet:
  //   Mateus Augusto Moraes Ferreira   Matricula:435669
endmodule

module Exemplo0074 (
  input  X,
  input  RESET,
  output S
);

  wire CLOCK_out, d_ff_1_q, d_ff_2_q, d_ff_3_q, not_1_out;

  Clock CLOCK (.out(CLOCK_out));
  D_Flip_Flop d_ff_1 (.clk(CLOCK_out), .D(X), .Q(d_ff_1_q), .reset(RESET));  // open: Qn, preset, en
  D_Flip_Flop d_ff_2 (.clk(CLOCK_out), .D(d_ff_1_q), .Q(d_ff_2_q), .reset(RESET));  // open: Qn, preset, en
  D_Flip_Flop d_ff_3 (.clk(CLOCK_out), .D(d_ff_2_q), .Q(d_ff_3_q), .reset(RESET));  // open: Qn, preset, en
  D_Flip_Flop d_ff_4 (.clk(CLOCK_out), .D(d_ff_3_q), .Q(d_ff_3_q), .reset(RESET));  // open: Qn, preset, en
  not not_1 (not_1_out, d_ff_1_q);
  and and_1 (S, d_ff_3_q, d_ff_3_q, d_ff_2_q, not_1_out);

  // Notes on the sheet:
  //   Mateus Augusto Moraes Ferreira   Matricula:435669
endmodule
