// Logisim project Exercicio0052.circ as structural Verilog: 1 circuit, main circuit main
module main (
  input  in_1,
  input  Reset,
  output out_3
);

  wire A_q, B_q, C_q, Clk_out, D_q, not_1_out;

  Clock Clk (.out(Clk_out));
  D_Flip_Flop A (.clk(Clk_out), .D(in_1), .Q(A_q), .reset(Reset));  // open: Qn, preset, en
  D_Flip_Flop B (.clk(Clk_out), .D(A_q), .Q(B_q), .reset(Reset));  // open: Qn, preset, en
  D_Flip_Flop C (.clk(Clk_out), .D(B_q), .Q(C_q), .reset(Reset));  // open: Qn, preset, en
  D_Flip_Flop D (.clk(Clk_out), .D(C_q), .Q(D_q), .reset(Reset));  // open: Qn, preset, en
  and S (out_3, D_q, C_q, not_1_out, A_q);
  not not_1 (not_1_out, B_q);
endmodule
