// Logisim project Exemplo0052.circ as structural Verilog: 1 circuit, main circuit main
module main (
  input  in_1,
  input  clear,
  output s1
);

  wire clock_out, d_ff_1_q, d_ff_2_q, d_ff_3_q, not_1_out;

  Clock clock (.out(clock_out));
  D_Flip_Flop d_ff_1 (.clk(clock_out), .D(in_1), .Q(d_ff_1_q), .reset(clear));  // open: Qn, preset, en
  D_Flip_Flop d_ff_2 (.clk(clock_out), .D(d_ff_1_q), .Q(d_ff_2_q), .reset(clear));  // open: Qn, preset, en
  D_Flip_Flop d_ff_3 (.clk(clock_out), .D(d_ff_2_q), .Q(d_ff_3_q), .reset(clear));  // open: Qn, preset, en
  not not_1 (not_1_out, d_ff_2_q);
  and and_1 (s1, d_ff_1_q, not_1_out, d_ff_3_q);
endmodule
