// Logisim project Exemplo0053.circ as structural Verilog: 1 circuit, main circuit main
module main (
  input  in_1,
  output out_2
);

  wire and_1_out, clock_1_out, d_ff_1_q, d_ff_3_q, d_ff_4_q, d_ff_5_q, not_1_out, not_2_out;

  Clock clock_1 (.out(clock_1_out));
  D_Flip_Flop d_ff_1 (.clk(clock_1_out), .D(in_1), .Q(d_ff_1_q));  // open: Qn, preset, en, reset
  D_Flip_Flop d_ff_2 (.clk(clock_1_out), .D(and_1_out), .Q(out_2));  // open: Qn, preset, en, reset
  D_Flip_Flop d_ff_3 (.clk(clock_1_out), .D(d_ff_1_q), .Q(d_ff_3_q));  // open: Qn, preset, en, reset
  not not_1 (not_1_out, d_ff_3_q);
  and and_1 (and_1_out, d_ff_1_q, not_1_out, d_ff_4_q, not_2_out);
  D_Flip_Flop d_ff_4 (.clk(clock_1_out), .D(d_ff_3_q), .Q(d_ff_4_q));  // open: Qn, preset, en, reset
  D_Flip_Flop d_ff_5 (.clk(clock_1_out), .D(d_ff_4_q), .Q(d_ff_5_q));  // open: Qn, preset, en, reset
  not not_2 (not_2_out, d_ff_5_q);
endmodule
