// Logisim project guia7.circ as structural Verilog: 3 circuits, main circuit Exemplo0052
module Exemplo0052 (
  input  in_1,
  output out_2
);

  wire clock_1_out, d_ff_1_q, d_ff_2_q, d_ff_3_q, not_1_out;

  Clock clock_1 (.out(clock_1_out));
  D_Flip_Flop d_ff_1 (.clk(clock_1_out), .D(in_1), .Q(d_ff_1_q));  // open: Qn, preset, en, reset
  D_Flip_Flop d_ff_2 (.clk(clock_1_out), .D(d_ff_1_q), .Q(d_ff_2_q));  // open: Qn, preset, en, reset
  D_Flip_Flop d_ff_3 (.clk(clock_1_out), .D(d_ff_2_q), .Q(d_ff_3_q));  // open: Qn, preset, en, reset
  not not_1 (not_1_out, d_ff_2_q);
  and and_1 (out_2, d_ff_3_q, not_1_out, d_ff_1_q);
endmodule

module Exemplo0053 (
  input  in_1,
  input  in_2
);

  wire and_1_out, clock_1_out, d_ff_1_q, d_ff_2_q, d_ff_3_q, d_ff_4_q, not_1_out, not_2_out;

  Clock clock_1 (.out(clock_1_out));
  D_Flip_Flop d_ff_1 (.clk(clock_1_out), .D(in_1), .Q(d_ff_1_q), .reset(in_2));  // open: Qn, preset, en
  D_Flip_Flop d_ff_2 (.clk(clock_1_out), .D(d_ff_1_q), .Q(d_ff_2_q), .reset(in_2));  // open: Qn, preset, en
  D_Flip_Flop d_ff_3 (.clk(clock_1_out), .D(d_ff_2_q), .Q(d_ff_3_q), .reset(in_2));  // open: Qn, preset, en
  D_Flip_Flop d_ff_4 (.clk(clock_1_out), .D(d_ff_3_q), .Q(d_ff_4_q), .reset(in_2));  // open: Qn, preset, en
  not not_1 (not_1_out, d_ff_3_q);
  and and_1 (and_1_out, d_ff_4_q, not_1_out, d_ff_2_q, not_2_out);
  not not_2 (not_2_out, d_ff_1_q);
  D_Flip_Flop d_ff_5 (.clk(clock_1_out), .D(and_1_out), .reset(in_2));  // open: Q, Qn, preset, en
endmodule

module Exemplo0054 (
  input  in_1,
  input  in_2
);

  wire and_1_out, clock_1_out, d_ff_1_q, d_ff_2_q, d_ff_3_q, d_ff_4_q, not_1_out;

  Clock clock_1 (.out(clock_1_out));
  D_Flip_Flop d_ff_1 (.clk(clock_1_out), .D(in_1), .Q(d_ff_1_q), .reset(in_2));  // open: Qn, preset, en
  D_Flip_Flop d_ff_2 (.clk(clock_1_out), .D(d_ff_1_q), .Q(d_ff_2_q), .reset(in_2));  // open: Qn, preset, en
  D_Flip_Flop d_ff_3 (.clk(clock_1_out), .D(d_ff_2_q), .Q(d_ff_3_q), .reset(in_2));  // open: Qn, preset, en
  D_Flip_Flop d_ff_4 (.clk(clock_1_out), .D(d_ff_3_q), .Q(d_ff_4_q), .reset(in_2));  // open: Qn, preset, en
  not not_1 (not_1_out, d_ff_4_q);
  and and_1 (and_1_out, not_1_out, d_ff_3_q, d_ff_2_q, d_ff_1_q);
  D_Flip_Flop d_ff_5 (.clk(clock_1_out), .D(and_1_out), .reset(in_2));  // open: Q, Qn, preset, en
endmodule
