// Logisim project Extra02.circ as structural Verilog: 1 circuit, main circuit main
module main (
  input  Clock,
  input  in_2,
  input  Reset,
  output out_4
);

  wire and_1_out, and_2_out, d_ff_1_q, d_ff_1_qn, d_ff_2_q, d_ff_2_qn, d_ff_3_q, d_ff_3_qn, d_ff_4_q,
       d_ff_4_qn;

  D_Flip_Flop d_ff_1 (.clk(Clock), .D(in_2), .Q(d_ff_1_q), .Qn(d_ff_1_qn), .reset(Reset));  // open: preset, en
  D_Flip_Flop d_ff_2 (.clk(Clock), .D(d_ff_1_q), .Q(d_ff_2_q), .Qn(d_ff_2_qn), .reset(Reset));  // open: preset, en
  D_Flip_Flop d_ff_3 (.clk(Clock), .D(d_ff_2_q), .Q(d_ff_3_q), .Qn(d_ff_3_qn), .reset(Reset));  // open: preset, en
  D_Flip_Flop d_ff_4 (.clk(Clock), .D(d_ff_3_q), .Q(d_ff_4_q), .Qn(d_ff_4_qn), .reset(Reset));  // open: preset, en
  and and_1 (and_1_out, d_ff_4_q, d_ff_3_q, d_ff_2_q, d_ff_1_q);
  and and_2 (and_2_out, d_ff_4_qn, d_ff_3_qn, d_ff_2_qn, d_ff_1_qn);
  or or_1 (out_4, and_1_out, and_2_out);
endmodule
