// Logisim project Exercicio01 & 04.circ as structural Verilog: 1 circuit, main circuit main
module main (
  input  in_1,
  input  in_2,
  output out_3,
  output out_4,
  output out_5,
  output out_6,
  output out_7
);

  wire clock_1_out, or_1_out;

  Clock clock_1 (.out(clock_1_out));
  D_Flip_Flop d_ff_1 (.clk(clock_1_out), .D(out_4), .Q(out_3), .reset(in_2));  // open: Qn, preset, en
  D_Flip_Flop d_ff_2 (.clk(clock_1_out), .D(out_5), .Q(out_4), .reset(in_2));  // open: Qn, preset, en
  or or_1 (or_1_out, in_1, out_3);
  D_Flip_Flop d_ff_3 (.clk(clock_1_out), .D(out_6), .Q(out_5), .reset(in_2));  // open: Qn, preset, en
  D_Flip_Flop d_ff_4 (.clk(clock_1_out), .D(out_7), .Q(out_6), .reset(in_2));  // open: Qn, preset, en
  D_Flip_Flop d_ff_5 (.clk(clock_1_out), .D(or_1_out), .Q(out_7), .reset(in_2));  // open: Qn, preset, en
endmodule
