// Logisim project Exercicio02.circ as structural Verilog: 1 circuit, main circuit main
module main (
  input  Reg,
  input  Clean,
  input  Load,
  output [4:0] out_4
);

  wire Clk_out, j_k_ff_2_qn, j_k_ff_3_qn, j_k_ff_4_qn, j_k_ff_5_qn, not_1_out, or_1_out, or_2_out, or_3_out,
       or_4_out, or_5_out;

  Clock Clk (.out(Clk_out));
  or or_1 (or_1_out, out_4[3], Load);
  J_K_Flip_Flop j_k_ff_1 (
    .J(or_1_out), .clk(Clk_out), .K(j_k_ff_2_qn), .Q(out_4[4]), .reset(Clean));  // open: Qn, preset, en
  or or_2 (or_2_out, out_4[2], Load);
  J_K_Flip_Flop j_k_ff_2 (
    .J(or_2_out), .clk(Clk_out), .K(j_k_ff_3_qn), .Q(out_4[3]), .Qn(j_k_ff_2_qn), .reset(Clean));  // open: preset, en
  or or_3 (or_3_out, out_4[1], Load);
  J_K_Flip_Flop j_k_ff_3 (
    .J(or_3_out), .clk(Clk_out), .K(j_k_ff_4_qn), .Q(out_4[2]), .Qn(j_k_ff_3_qn), .reset(Clean));  // open: preset, en
  or or_4 (or_4_out, out_4[0], Load);
  J_K_Flip_Flop j_k_ff_4 (
    .J(or_4_out), .clk(Clk_out), .K(j_k_ff_5_qn), .Q(out_4[1]), .Qn(j_k_ff_4_qn), .reset(Clean));  // open: preset, en
  or or_5 (or_5_out, Load, Reg);
  J_K_Flip_Flop j_k_ff_5 (
    .J(or_5_out), .clk(Clk_out), .K(not_1_out), .Q(out_4[0]), .Qn(j_k_ff_5_qn), .reset(Clean));  // open: preset, en
  not not_1 (not_1_out, or_5_out);
endmodule
