// Logisim project Exercicio03.circ as structural Verilog: 1 circuit, main circuit main
module main (
  input  Reg,
  input  Clean,
  output [4:0] out_3
);

  wire clock_1_out, or_1_out;

  Clock clock_1 (.out(clock_1_out));
  or or_1 (or_1_out, Reg, out_3[0]);
  D_Flip_Flop d_ff_1 (.clk(clock_1_out), .D(or_1_out), .Q(out_3[4]), .reset(Clean));  // open: Qn, preset, en
  D_Flip_Flop d_ff_2 (.clk(clock_1_out), .D(out_3[4]), .Q(out_3[3]), .reset(Clean));  // open: Qn, preset, en
  D_Flip_Flop d_ff_3 (.clk(clock_1_out), .D(out_3[3]), .Q(out_3[2]), .reset(Clean));  // open: Qn, preset, en
  D_Flip_Flop d_ff_4 (.clk(clock_1_out), .D(out_3[2]), .Q(out_3[1]), .reset(Clean));  // open: Qn, preset, en
  D_Flip_Flop d_ff_5 (.clk(clock_1_out), .D(out_3[1]), .Q(out_3[0]), .reset(Clean));  // open: Qn, preset, en
endmodule
