// Logisim project (Left) Shift register (D).circ as structural Verilog: 1 circuit, main circuit main
module main (
  input  data,
  input  clear,
  output A,
  output B,
  output C,
  output D,
  output E
);

  wire clk_out;

  Clock clk (.out(clk_out));
  D_Flip_Flop d_ff_1 (.clk(clk_out), .D(B), .Q(A), .reset(clear));  // open: Qn, preset, en
  D_Flip_Flop d_ff_2 (.clk(clk_out), .D(C), .Q(B), .reset(clear));  // open: Qn, preset, en
  D_Flip_Flop d_ff_3 (.clk(clk_out), .D(D), .Q(C), .reset(clear));  // open: Qn, preset, en
  D_Flip_Flop d_ff_4 (.clk(clk_out), .D(E), .Q(D), .reset(clear));  // open: Qn, preset, en
  D_Flip_Flop d_ff_5 (.clk(clk_out), .D(data), .Q(E), .reset(clear));  // open: Qn, preset, en

  // Notes on the sheet:
  //   (Left) Shift register (D)
endmodule
