// Logisim project Pararel_in_Serial_out.circ as structural Verilog: 1 circuit, main circuit main
module main (
  input  clr,
  input  ld,
  input  in_3,
  input  in_4,
  input  in_5,
  input  in_6,
  input  in_7,
  output a,
  output b,
  output c,
  output d,
  output e
);

  wire and_1_out, and_2_out, and_3_out, and_4_out, and_5_out, clk_out;

  Clock clk (.out(clk_out));
  and and_1 (and_1_out, ld, in_3);
  D_Flip_Flop d_ff_1 (.clk(clk_out), .Q(a), .preset(and_1_out), .reset(clr));  // open: D, Qn, en
  and and_2 (and_2_out, ld, in_4);
  D_Flip_Flop d_ff_2 (.clk(clk_out), .D(a), .Q(b), .preset(and_2_out), .reset(clr));  // open: Qn, en
  D_Flip_Flop d_ff_3 (.clk(clk_out), .D(b), .Q(c), .preset(and_3_out), .reset(clr));  // open: Qn, en
  and and_3 (and_3_out, ld, in_5);
  D_Flip_Flop d_ff_4 (.clk(clk_out), .D(c), .Q(d), .preset(and_4_out), .reset(clr));  // open: Qn, en
  and and_4 (and_4_out, ld, in_6);
  D_Flip_Flop d_ff_5 (.clk(clk_out), .D(d), .Q(e), .preset(and_5_out), .reset(clr));  // open: Qn, en
  and and_5 (and_5_out, ld, in_7);

  // Notes on the sheet:
  //   Paralel_In/Serial_Out
endmodule
