// Logisim project registrador de deslocamento circular para a direita.circ as structural Verilog: 1 circuit, main circuit main
module main (
  input  \input ,
  input  clear,
  output A,
  output B,
  output C,
  output D,
  output E
);

  wire clk_out, or_1_out;

  Clock clk (.out(clk_out));
  or or_1 (or_1_out, E, \input );
  D_Flip_Flop d_ff_1 (.clk(clk_out), .D(or_1_out), .Q(A), .reset(clear));  // open: Qn, preset, en
  D_Flip_Flop d_ff_2 (.clk(clk_out), .D(A), .Q(B), .reset(clear));  // open: Qn, preset, en
  D_Flip_Flop d_ff_3 (.clk(clk_out), .D(B), .Q(C), .reset(clear));  // open: Qn, preset, en
  D_Flip_Flop d_ff_4 (.clk(clk_out), .D(C), .Q(D), .reset(clear));  // open: Qn, preset, en
  D_Flip_Flop d_ff_5 (.clk(clk_out), .D(D), .Q(E), .reset(clear));  // open: Qn, preset, en

  // Notes on the sheet:
  //   Registrador de Deslocamento Circular para Direita
endmodule
