// Logisim project Exercicio03.circ as structural Verilog: 1 circuit, main circuit main
module main (
  input  CLK,
  input  Data,
  input  Clr,
  input  Carga,
  output a,
  output b,
  output c,
  output d,
  output e
);

  D_Flip_Flop d_ff_1 (.clk(CLK), .D(Data), .Q(a), .preset(Carga), .reset(Clr));  // open: Qn, en
  D_Flip_Flop d_ff_2 (.clk(CLK), .D(a), .Q(b), .reset(Clr));  // open: Qn, preset, en
  D_Flip_Flop d_ff_3 (.clk(CLK), .D(b), .Q(c), .reset(Clr));  // open: Qn, preset, en
  D_Flip_Flop d_ff_4 (.clk(CLK), .D(c), .Q(d), .reset(Clr));  // open: Qn, preset, en
  D_Flip_Flop d_ff_5 (.clk(CLK), .D(d), .Q(e), .reset(Clr));  // open: Qn, preset, en

  // Notes on the sheet:
  //   Nome: Jorge Luis - Deslocador para direita 5 bits
endmodule
