// Logisim project Exercicio04.circ as structural Verilog: 1 circuit, main circuit main
module main (
  input  Data,
  input  Clr,
  input  Carga,
  output a,
  output b,
  output c,
  output d,
  output e
);

  wire Clock_out, or_01_out;

  Clock Clock (.out(Clock_out));
  or or_01 (or_01_out, a, Data);
  D_Flip_Flop d_ff_1 (.clk(Clock_out), .D(b), .Q(a), .preset(Carga), .reset(Clr));  // open: Qn, en
  D_Flip_Flop d_ff_2 (.clk(Clock_out), .D(c), .Q(b), .reset(Clr));  // open: Qn, preset, en
  D_Flip_Flop d_ff_3 (.clk(Clock_out), .D(e), .Q(d), .reset(Clr));  // open: Qn, preset, en
  D_Flip_Flop d_ff_4 (.clk(Clock_out), .D(d), .Q(c), .reset(Clr));  // open: Qn, preset, en
  D_Flip_Flop d_ff_5 (.clk(Clock_out), .D(or_01_out), .Q(e), .reset(Clr));  // open: Qn, preset, en

  // Notes on the sheet:
  //   Nome: Jorge Luis - Deslocador para esquerda 5 bits em anel torcido
endmodule
