// Logisim project Exercicio01.circ as structural Verilog: 1 circuit, main circuit main
// Desslocamento Para A Esquerda
module main (
  input  in_1,
  input  in_2,
  output out_3,
  output out_4,
  output out_5,
  output out_6
);

  wire clock_1_out;

  Clock clock_1 (.out(clock_1_out));
  D_Flip_Flop d_ff_1 (.clk(clock_1_out), .D(out_4), .Q(out_3), .en(in_2));  // open: Qn, preset, reset
  D_Flip_Flop d_ff_2 (.clk(out_5), .D(clock_1_out), .Q(out_4), .en(in_2));  // open: Qn, preset, reset
  D_Flip_Flop d_ff_3 (.clk(clock_1_out), .D(out_6), .Q(out_5), .en(in_2));  // open: Qn, preset, reset
  D_Flip_Flop d_ff_4 (.clk(clock_1_out), .Q(out_6), .reset(in_2));  // open: D, Qn, preset, en
  D_Flip_Flop d_ff_5 (.clk(clock_1_out), .D(in_1), .reset(in_2));  // open: Q, Qn, preset, en
endmodule
