// Logisim project Exericicio04.circ as structural Verilog: 1 circuit, main circuit main
module main (
  input  in_1,
  input  in_2,
  output out_3,
  output out_4,
  output out_5,
  output out_6,
  output out_7
);

  wire or_1_out;

  Clock clock_1 (.out(out_5));
  or or_1 (or_1_out, out_3, in_1);
  D_Flip_Flop d_ff_1 (.clk(out_5), .D(out_4), .Q(out_3), .reset(in_2));  // open: Qn, preset, en
  D_Flip_Flop d_ff_2 (.clk(out_5), .D(out_5), .Q(out_4), .reset(in_2));  // open: Qn, preset, en
  D_Flip_Flop d_ff_3 (.clk(out_5), .D(out_5), .Q(out_4), .reset(in_2));  // open: Qn, preset, en
  D_Flip_Flop d_ff_4 (.clk(out_5), .D(out_5), .Q(out_5), .reset(in_2));  // open: Qn, preset, en
  D_Flip_Flop d_ff_5 (.clk(out_5), .D(or_1_out), .Q(out_5), .reset(in_2));  // open: Qn, preset, en

  assign out_6 = out_5;
  assign out_7 = out_5;

  // Notes on the sheet:
  //   Registrador Circular Com Carga Inicia Para Esqerda
endmodule
