// Logisim project Circuitos.circ as structural Verilog: 1 circuit, main circuit main
module main (
  input  dt,
  input  reset,
  input  dt_2,
  input  reset_2,
  input  in_5,
  input  in_6,
  output out_7,
  output out_8,
  output out_9,
  output out_10,
  output out_11,
  output out_12,
  output out_13,
  output out_14,
  output out_15,
  output out_16,
  output out_17,
  output out_18,
  output out_19,
  output out_20
);

  wire clock_1_out, clock_2_out, clock_3_out, d_ff_15_q, or_1_out, or_2_out, or_3_out, or_4_out, or_5_out;

  Clock clock_1 (.out(clock_1_out));
  Clock clock_2 (.out(clock_2_out));
  Clock clock_3 (.out(clock_3_out));
  or or_1 (or_1_out, out_13, dt_2);
  D_Flip_Flop d_ff_1 (.clk(clock_1_out), .D(out_8), .Q(out_7), .reset(reset));  // open: Qn, preset, en
  or or_2 (or_2_out, dt, out_7);
  D_Flip_Flop d_ff_2 (.clk(clock_2_out), .D(or_1_out), .Q(out_12), .reset(reset_2));  // open: Qn, preset, en
  D_Flip_Flop d_ff_3 (.clk(clock_3_out), .D(in_5), .Q(out_16), .reset(in_6));  // open: Qn, preset, en
  D_Flip_Flop d_ff_4 (.clk(clock_1_out), .D(out_9), .Q(out_8), .reset(reset));  // open: Qn, preset, en
  or or_3 (or_3_out, out_14, dt_2);
  D_Flip_Flop d_ff_5 (.clk(clock_3_out), .D(out_16), .Q(out_17), .reset(in_6));  // open: Qn, preset, en
  D_Flip_Flop d_ff_6 (.clk(clock_1_out), .D(out_10), .Q(out_9), .reset(reset));  // open: Qn, preset, en
  D_Flip_Flop d_ff_7 (.clk(clock_2_out), .D(or_3_out), .Q(out_13), .reset(reset_2));  // open: Qn, preset, en
  D_Flip_Flop d_ff_8 (.clk(clock_3_out), .D(out_17), .Q(out_18), .reset(in_6));  // open: Qn, preset, en
  D_Flip_Flop d_ff_9 (.clk(clock_1_out), .D(out_11), .Q(out_10), .reset(reset));  // open: Qn, preset, en
  D_Flip_Flop d_ff_10 (.clk(clock_2_out), .D(or_4_out), .Q(out_14), .reset(reset_2));  // open: Qn, preset, en
  or or_4 (or_4_out, out_15, dt_2);
  D_Flip_Flop d_ff_11 (.clk(clock_3_out), .D(out_18), .Q(out_19), .reset(in_6));  // open: Qn, preset, en
  D_Flip_Flop d_ff_12 (.clk(clock_1_out), .D(or_2_out), .Q(out_11), .reset(reset));  // open: Qn, preset, en
  or or_5 (or_5_out, d_ff_15_q, dt_2);
  D_Flip_Flop d_ff_13 (.clk(clock_3_out), .D(out_19), .Q(out_20), .reset(in_6));  // open: Qn, preset, en
  D_Flip_Flop d_ff_14 (.clk(clock_2_out), .D(or_5_out), .Q(out_15), .reset(reset_2));  // open: Qn, preset, en
  D_Flip_Flop d_ff_15 (.clk(clock_2_out), .D(dt_2), .Q(d_ff_15_q), .reset(reset_2));  // open: Qn, preset, en

  // Notes on the sheet:
  //   clock
  //   clock
  //   Lorena Danielle Gonçalves Bento -435049
endmodule
