// Logisim project Exercicio001.circ as structural Verilog: 1 circuit, main circuit main
module main (
  input  in_1,
  input  CLR,
  input  LD,
  input  Q0,
  output out_5,
  output out_6,
  output out_7,
  output out_8,
  output out_9
);

  wire and_1_out, CLK_out;

  Clock CLK (.out(CLK_out));
  D_Flip_Flop d_ff_1 (.clk(CLK_out), .D(out_6), .Q(out_5), .reset(CLR));  // open: Qn, preset, en
  D_Flip_Flop d_ff_2 (.clk(CLK_out), .D(out_7), .Q(out_6), .reset(CLR));  // open: Qn, preset, en
  D_Flip_Flop d_ff_3 (.clk(CLK_out), .D(out_8), .Q(out_7), .reset(CLR));  // open: Qn, preset, en
  D_Flip_Flop d_ff_4 (.clk(CLK_out), .D(out_9), .Q(out_8), .reset(CLR));  // open: Qn, preset, en
  D_Flip_Flop d_ff_5 (.clk(CLK_out), .D(in_1), .Q(out_9), .preset(and_1_out), .reset(CLR));  // open: Qn, en
  and and_1 (and_1_out, LD, Q0);
endmodule
