// Logisim project Exercicio002.circ as structural Verilog: 1 circuit, main circuit main
module main (
  input  in_1,
  input  CLR,
  input  LD,
  input  Q4,
  input  Q3,
  input  Q2,
  input  Q1,
  input  Q0,
  output out_9,
  output out_10,
  output out_11,
  output out_12,
  output out_13
);

  wire and_1_out, and_2_out, and_3_out, and_4_out, and_5_out, CLK_out;

  Clock CLK (.out(CLK_out));
  D_Flip_Flop d_ff_1 (.clk(CLK_out), .D(out_10), .Q(out_9), .preset(and_1_out), .reset(CLR));  // open: Qn, en
  and and_1 (and_1_out, Q4, LD);
  D_Flip_Flop d_ff_2 (.clk(CLK_out), .D(out_11), .Q(out_10), .preset(and_2_out), .reset(CLR));  // open: Qn, en
  and and_2 (and_2_out, Q3, LD);
  D_Flip_Flop d_ff_3 (.clk(CLK_out), .D(out_12), .Q(out_11), .preset(and_3_out), .reset(CLR));  // open: Qn, en
  and and_3 (and_3_out, Q2, LD);
  D_Flip_Flop d_ff_4 (.clk(CLK_out), .D(out_13), .Q(out_12), .preset(and_4_out), .reset(CLR));  // open: Qn, en
  and and_4 (and_4_out, LD, Q1);
  D_Flip_Flop d_ff_5 (.clk(CLK_out), .D(in_1), .Q(out_13), .preset(and_5_out), .reset(CLR));  // open: Qn, en
  and and_5 (and_5_out, LD, Q0);
endmodule
