// Logisim project Guia08.circ as structural Verilog: 1 circuit, main circuit main
module main (
  input  in_1,
  input  in_2,
  input  in_3,
  input  in_4,
  input  in_5,
  input  in_6,
  input  in_7,
  input  in_8,
  input  in_9,
  input  in_10,
  output out_11,
  output out_12,
  output out_13,
  output out_14,
  output out_15,
  output out_16,
  output out_17,
  output out_18,
  output out_19,
  output out_20,
  output out_21,
  output out_22,
  output out_23,
  output out_24,
  output out_25,
  output out_26,
  output out_27,
  output out_28,
  output out_29,
  output out_30
);

  wire and_1_out, and_2_out, and_3_out, and_4_out, and_5_out, clock_1_out, clock_2_out, clock_3_out,
       clock_4_out, or_1_out;

  Clock clock_1 (.out(clock_1_out));
  Clock clock_2 (.out(clock_2_out));
  Clock clock_3 (.out(clock_3_out));
  Clock clock_4 (.out(clock_4_out));
  and and_1 (and_1_out, in_5, in_6);
  D_Flip_Flop d_ff_1 (.clk(clock_1_out), .D(out_12), .Q(out_11));  // open: Qn, preset, en, reset
  D_Flip_Flop d_ff_2 (.clk(clock_2_out), .D(in_2), .Q(out_16));  // open: Qn, preset, en, reset
  D_Flip_Flop d_ff_3 (.clk(clock_3_out), .D(out_22), .Q(out_21));  // open: Qn, preset, en, reset
  D_Flip_Flop d_ff_4 (.clk(clock_4_out), .Q(out_26), .preset(and_1_out), .reset(in_4));  // open: D, Qn, en
  and and_2 (and_2_out, in_5, in_7);
  D_Flip_Flop d_ff_5 (.clk(clock_1_out), .D(out_13), .Q(out_12));  // open: Qn, preset, en, reset
  D_Flip_Flop d_ff_6 (.clk(clock_2_out), .D(out_16), .Q(out_17));  // open: Qn, preset, en, reset
  D_Flip_Flop d_ff_7 (.clk(clock_3_out), .D(out_23), .Q(out_22));  // open: Qn, preset, en, reset
  or or_1 (or_1_out, out_21, in_3);
  D_Flip_Flop d_ff_8 (.clk(clock_4_out), .D(out_26), .Q(out_27), .preset(and_2_out), .reset(in_4));  // open: Qn, en
  and and_3 (and_3_out, in_5, in_8);
  D_Flip_Flop d_ff_9 (.clk(clock_1_out), .D(out_14), .Q(out_13));  // open: Qn, preset, en, reset
  D_Flip_Flop d_ff_10 (.clk(clock_2_out), .D(out_17), .Q(out_18));  // open: Qn, preset, en, reset
  D_Flip_Flop d_ff_11 (.clk(clock_3_out), .D(out_24), .Q(out_23));  // open: Qn, preset, en, reset
  D_Flip_Flop d_ff_12 (.clk(clock_4_out), .D(out_27), .Q(out_28), .preset(and_3_out), .reset(in_4));  // open: Qn, en
  D_Flip_Flop d_ff_13 (.clk(clock_1_out), .D(out_15), .Q(out_14));  // open: Qn, preset, en, reset
  D_Flip_Flop d_ff_14 (.clk(clock_2_out), .D(out_18), .Q(out_19));  // open: Qn, preset, en, reset
  D_Flip_Flop d_ff_15 (.clk(clock_3_out), .D(out_25), .Q(out_24));  // open: Qn, preset, en, reset
  D_Flip_Flop d_ff_16 (.clk(clock_4_out), .D(out_28), .Q(out_29), .preset(and_4_out), .reset(in_4));  // open: Qn, en
  and and_4 (and_4_out, in_5, in_9);
  D_Flip_Flop d_ff_17 (.clk(clock_1_out), .D(in_1), .Q(out_15));  // open: Qn, preset, en, reset
  D_Flip_Flop d_ff_18 (.clk(clock_2_out), .D(out_19), .Q(out_20));  // open: Qn, preset, en, reset
  D_Flip_Flop d_ff_19 (.clk(clock_3_out), .D(or_1_out), .Q(out_25));  // open: Qn, preset, en, reset
  D_Flip_Flop d_ff_20 (.clk(clock_4_out), .D(out_29), .Q(out_30), .preset(and_5_out), .reset(in_4));  // open: Qn, en
  and and_5 (and_5_out, in_5, in_10);
endmodule
