// Logisim project Circuitos.circ as structural Verilog: 4 circuits, main circuit 1
module _1 (
  input  in_1,
  output out_2,
  output out_3,
  output out_4,
  output out_5,
  output out_6
);

  wire CLK_out;

  Clock CLK (.out(CLK_out));
  D_Flip_Flop d_ff_1 (.clk(CLK_out), .D(out_3), .Q(out_2));  // open: Qn, preset, en, reset
  D_Flip_Flop d_ff_2 (.clk(CLK_out), .D(out_4), .Q(out_3));  // open: Qn, preset, en, reset
  D_Flip_Flop d_ff_3 (.clk(CLK_out), .D(out_5), .Q(out_4));  // open: Qn, preset, en, reset
  D_Flip_Flop d_ff_4 (.clk(CLK_out), .D(out_6), .Q(out_5));  // open: Qn, preset, en, reset
  D_Flip_Flop d_ff_5 (.clk(CLK_out), .D(in_1), .Q(out_6));  // open: Qn, preset, en, reset

  // Notes on the sheet:
  //   Mateus Augusto Moraes Ferreira   Matricula: 435669
endmodule

module _2 (
  input  in_1,
  output out_2,
  output out_3,
  output out_4,
  output out_5,
  output out_6
);

  wire CLK_out;

  Clock CLK (.out(CLK_out));
  D_Flip_Flop d_ff_1 (.clk(CLK_out), .D(in_1), .Q(out_2));  // open: Qn, preset, en, reset
  D_Flip_Flop d_ff_2 (.clk(CLK_out), .D(out_2), .Q(out_3));  // open: Qn, preset, en, reset
  D_Flip_Flop d_ff_3 (.clk(CLK_out), .D(out_3), .Q(out_4));  // open: Qn, preset, en, reset
  D_Flip_Flop d_ff_4 (.clk(CLK_out), .D(out_4), .Q(out_5));  // open: Qn, preset, en, reset
  D_Flip_Flop d_ff_5 (.clk(CLK_out), .D(out_5), .Q(out_6));  // open: Qn, preset, en, reset

  // Notes on the sheet:
  //   Mateus Augusto Moraes Ferreira   Matricula: 435669
endmodule

module _3 (
  input  in_1,
  output out_2,
  output out_3,
  output out_4,
  output out_5,
  output out_6
);

  wire CLK_out, or_1_out;

  Clock CLK (.out(CLK_out));
  D_Flip_Flop d_ff_1 (.clk(CLK_out), .D(out_3), .Q(out_2));  // open: Qn, preset, en, reset
  D_Flip_Flop d_ff_2 (.clk(CLK_out), .D(out_4), .Q(out_3));  // open: Qn, preset, en, reset
  or or_1 (or_1_out, out_2, in_1);
  D_Flip_Flop d_ff_3 (.clk(CLK_out), .D(out_5), .Q(out_4));  // open: Qn, preset, en, reset
  D_Flip_Flop d_ff_4 (.clk(CLK_out), .D(out_6), .Q(out_5));  // open: Qn, preset, en, reset
  D_Flip_Flop d_ff_5 (.clk(CLK_out), .D(or_1_out), .Q(out_6));  // open: Qn, preset, en, reset

  // Notes on the sheet:
  //   Mateus Augusto Moraes Ferreira   Matricula: 435669
endmodule

module _4 (
  input  in_1,
  input  in_2,
  input  in_3,
  input  in_4,
  input  in_5,
  input  in_6,
  input  in_7,
  output out_8,
  output out_9,
  output out_10,
  output out_11,
  output out_12
);

  wire and_1_out, and_2_out, and_3_out, and_4_out, and_5_out, CLK_out;

  Clock CLK (.out(CLK_out));
  D_Flip_Flop d_ff_1 (.clk(CLK_out), .Q(out_8), .preset(and_1_out), .reset(in_1));  // open: D, Qn, en
  and and_1 (and_1_out, in_2, in_3);
  D_Flip_Flop d_ff_2 (.clk(CLK_out), .D(out_8), .Q(out_9), .preset(and_2_out), .reset(in_1));  // open: Qn, en
  and and_2 (and_2_out, in_2, in_4);
  D_Flip_Flop d_ff_3 (.clk(CLK_out), .D(out_9), .Q(out_10), .preset(and_3_out), .reset(in_1));  // open: Qn, en
  and and_3 (and_3_out, in_2, in_5);
  D_Flip_Flop d_ff_4 (.clk(CLK_out), .D(out_10), .Q(out_11), .preset(and_4_out), .reset(in_1));  // open: Qn, en
  and and_4 (and_4_out, in_2, in_6);
  D_Flip_Flop d_ff_5 (.clk(CLK_out), .D(out_11), .Q(out_12), .preset(and_5_out), .reset(in_1));  // open: Qn, en
  and and_5 (and_5_out, in_2, in_7);

  // Notes on the sheet:
  //   Mateus Augusto Moraes Ferreira   Matricula: 435669
endmodule
