// Logisim project circuitos.circ as structural Verilog: 4 circuits, main circuit esq
module esq (
  input  Clock,
  input  Dado,
  input  Clear,
  output out_4,
  output out_5,
  output out_6,
  output out_7,
  output out_8
);

  D_Flip_Flop d_ff_1 (.clk(Clock), .D(out_5), .Q(out_4), .reset(Clear));  // open: Qn, preset, en
  D_Flip_Flop d_ff_2 (.clk(Clock), .D(out_6), .Q(out_5), .reset(Clear));  // open: Qn, preset, en
  D_Flip_Flop d_ff_3 (.clk(Clock), .D(out_7), .Q(out_6), .reset(Clear));  // open: Qn, preset, en
  D_Flip_Flop d_ff_4 (.clk(Clock), .D(out_8), .Q(out_7), .reset(Clear));  // open: Qn, preset, en
  D_Flip_Flop d_ff_5 (.clk(Clock), .D(Dado), .Q(out_8), .reset(Clear));  // open: Qn, preset, en

  // Notes on the sheet:
  //   Esquerda
endmodule

module circ_dir (
  input  Clock,
  input  Dado,
  input  Clear,
  output out_4,
  output out_5,
  output out_6,
  output out_7,
  output out_8
);

  wire or_1_out;

  D_Flip_Flop d_ff_1 (.clk(Clock), .D(or_1_out), .Q(out_4), .reset(Clear));  // open: Qn, preset, en
  or or_1 (or_1_out, out_8, Dado);
  D_Flip_Flop d_ff_2 (.clk(Clock), .D(out_4), .Q(out_5), .reset(Clear));  // open: Qn, preset, en
  D_Flip_Flop d_ff_3 (.clk(Clock), .D(out_5), .Q(out_6), .reset(Clear));  // open: Qn, preset, en
  D_Flip_Flop d_ff_4 (.clk(Clock), .D(out_6), .Q(out_7), .reset(Clear));  // open: Qn, preset, en
  D_Flip_Flop d_ff_5 (.clk(Clock), .D(out_7), .Q(out_8), .reset(Clear));  // open: Qn, preset, en

  // Notes on the sheet:
  //   Circular para a direita
endmodule

module circ_esq (
  input  Clock,
  input  Dado,
  input  Clear,
  output out_4,
  output out_5,
  output out_6,
  output out_7,
  output out_8
);

  wire or_1_out;

  or or_1 (or_1_out, out_4, Dado);
  D_Flip_Flop d_ff_1 (.clk(Clock), .D(out_5), .Q(out_4), .reset(Clear));  // open: Qn, preset, en
  D_Flip_Flop d_ff_2 (.clk(Clock), .D(out_6), .Q(out_5), .reset(Clear));  // open: Qn, preset, en
  D_Flip_Flop d_ff_3 (.clk(Clock), .D(out_7), .Q(out_6), .reset(Clear));  // open: Qn, preset, en
  D_Flip_Flop d_ff_4 (.clk(Clock), .D(out_8), .Q(out_7), .reset(Clear));  // open: Qn, preset, en
  D_Flip_Flop d_ff_5 (.clk(Clock), .D(or_1_out), .Q(out_8), .reset(Clear));  // open: Qn, preset, en

  // Notes on the sheet:
  //   Circular para a esquerda
endmodule

module dir (
  input  Clock,
  input  Dado,
  input  Clear,
  output out_4,
  output out_5,
  output out_6,
  output out_7,
  output out_8
);

  D_Flip_Flop d_ff_1 (.clk(Clock), .D(Dado), .Q(out_4), .reset(Clear));  // open: Qn, preset, en
  D_Flip_Flop d_ff_2 (.clk(Clock), .D(out_4), .Q(out_5), .reset(Clear));  // open: Qn, preset, en
  D_Flip_Flop d_ff_3 (.clk(Clock), .D(out_5), .Q(out_6), .reset(Clear));  // open: Qn, preset, en
  D_Flip_Flop d_ff_4 (.clk(Clock), .D(out_6), .Q(out_7), .reset(Clear));  // open: Qn, preset, en
  D_Flip_Flop d_ff_5 (.clk(Clock), .D(out_7), .Q(out_8), .reset(Clear));  // open: Qn, preset, en

  // Notes on the sheet:
  //   Direita
endmodule
