// Logisim project guia08.circ as structural Verilog
module Exemplo0061 (
  input  Data,
  input  Clear,
  output out_3,
  output out_4,
  output out_5,
  output out_6,
  output out_7
);

  wire clock_1_out;

  Clock clock_1 (.out(clock_1_out));
  D_Flip_Flop d_ff_1 (.clk(clock_1_out), .D(out_4), .Q(out_3), .reset(Clear));  // open: Qn, preset, en
  D_Flip_Flop d_ff_2 (.clk(clock_1_out), .D(out_5), .Q(out_4), .reset(Clear));  // open: Qn, preset, en
  D_Flip_Flop d_ff_3 (.clk(clock_1_out), .D(out_6), .Q(out_5), .reset(Clear));  // open: Qn, preset, en
  D_Flip_Flop d_ff_4 (.clk(clock_1_out), .D(out_7), .Q(out_6), .reset(Clear));  // open: Qn, preset, en
  D_Flip_Flop d_ff_5 (.clk(clock_1_out), .D(Data), .Q(out_7), .reset(Clear));  // open: Qn, preset, en
endmodule

module Exemplo0062 (
  input  Data,
  input  Clear,
  output out_3,
  output out_4,
  output out_5,
  output out_6,
  output out_7
);

  wire clock_1_out, or_1_out, or_2_out, or_3_out, or_4_out;

  Clock clock_1 (.out(clock_1_out));
  or or_1 (or_1_out, out_4, Data);
  D_Flip_Flop d_ff_1 (.clk(clock_1_out), .D(or_1_out), .Q(out_3), .reset(Clear));  // open: Qn, preset, en
  D_Flip_Flop d_ff_2 (.clk(clock_1_out), .D(or_2_out), .Q(out_4), .reset(Clear));  // open: Qn, preset, en
  or or_2 (or_2_out, out_5, Data);
  or or_3 (or_3_out, out_6, Data);
  D_Flip_Flop d_ff_3 (.clk(clock_1_out), .D(or_3_out), .Q(out_5), .reset(Clear));  // open: Qn, preset, en
  or or_4 (or_4_out, out_7, Data);
  D_Flip_Flop d_ff_4 (.clk(clock_1_out), .D(or_4_out), .Q(out_6), .reset(Clear));  // open: Qn, preset, en
  D_Flip_Flop d_ff_5 (.clk(clock_1_out), .D(Data), .Q(out_7), .reset(Clear));  // open: Qn, preset, en
endmodule

module Exemplo0063 (
  input  Data,
  input  Clear,
  output out_3,
  output out_4,
  output out_5,
  output out_6,
  output out_7
);

  wire clock_1_out, or_1_out;

  Clock clock_1 (.out(clock_1_out));
  or or_1 (or_1_out, out_7, Data);
  D_Flip_Flop d_ff_1 (.clk(clock_1_out), .D(or_1_out), .Q(out_3), .reset(Clear));  // open: Qn, preset, en
  D_Flip_Flop d_ff_2 (.clk(clock_1_out), .D(out_3), .Q(out_4), .reset(Clear));  // open: Qn, preset, en
  D_Flip_Flop d_ff_3 (.clk(clock_1_out), .D(out_4), .Q(out_5), .reset(Clear));  // open: Qn, preset, en
  D_Flip_Flop d_ff_4 (.clk(clock_1_out), .D(out_5), .Q(out_6), .reset(Clear));  // open: Qn, preset, en
  D_Flip_Flop d_ff_5 (.clk(clock_1_out), .D(out_6), .Q(out_7), .reset(Clear));  // open: Qn, preset, en
endmodule

module Exemplo0064 (
  input  Data,
  input  Clear,
  output out_3,
  output out_4,
  output out_5,
  output out_6,
  output out_7
);

  wire clock_1_out, d_ff_1_qn, or_1_out;

  Clock clock_1 (.out(clock_1_out));
  D_Flip_Flop d_ff_1 (.clk(clock_1_out), .D(out_4), .Q(out_3), .Qn(d_ff_1_qn), .reset(Clear));  // open: preset, en
  D_Flip_Flop d_ff_2 (.clk(clock_1_out), .D(out_5), .Q(out_4), .reset(Clear));  // open: Qn, preset, en
  D_Flip_Flop d_ff_3 (.clk(clock_1_out), .D(out_6), .Q(out_5), .reset(Clear));  // open: Qn, preset, en
  D_Flip_Flop d_ff_4 (.clk(clock_1_out), .D(out_7), .Q(out_6), .reset(Clear));  // open: Qn, preset, en
  D_Flip_Flop d_ff_5 (.clk(clock_1_out), .D(or_1_out), .Q(out_7), .reset(Clear));  // open: Qn, preset, en
  or or_1 (or_1_out, d_ff_1_qn, Data);
endmodule

module Exemplo0065 (
  input  Clear,
  input  Load,
  input  in_3,
  input  in_4,
  input  in_5,
  input  in_6,
  input  in_7,
  output out_8,
  output out_9,
  output out_10,
  output out_11,
  output out_12
);

  wire and_1_out, and_2_out, and_3_out, and_4_out, and_5_out, clock_1_out;

  Clock clock_1 (.out(clock_1_out));
  D_Flip_Flop d_ff_1 (.clk(clock_1_out), .D(1'b0), .Q(out_8), .preset(and_1_out), .reset(Clear));  // open: Qn, en
  and and_1 (and_1_out, in_3, Load);
  D_Flip_Flop d_ff_2 (.clk(clock_1_out), .D(out_8), .Q(out_9), .preset(and_2_out), .reset(Clear));  // open: Qn, en
  and and_2 (and_2_out, in_4, Load);
  D_Flip_Flop d_ff_3 (.clk(clock_1_out), .D(out_9), .Q(out_10), .preset(and_3_out), .reset(Clear));  // open: Qn, en
  and and_3 (and_3_out, in_5, Load);
  D_Flip_Flop d_ff_4 (.clk(clock_1_out), .D(out_10), .Q(out_11), .preset(and_4_out), .reset(Clear));  // open: Qn, en
  and and_4 (and_4_out, in_6, Load);
  D_Flip_Flop d_ff_5 (.clk(clock_1_out), .D(out_11), .Q(out_12), .preset(and_5_out), .reset(Clear));  // open: Qn, en
  and and_5 (and_5_out, in_7, Load);
endmodule

module Exemplo0066 (
  input  Data,
  input  Clear,
  output out_3,
  output out_4,
  output out_5,
  output out_6,
  output out_7
);

  wire clock_1_out, or_1_out, or_2_out, or_3_out, or_4_out, or_5_out;

  Clock clock_1 (.out(clock_1_out));
  or or_1 (or_1_out, out_7, Data);
  D_Flip_Flop d_ff_1 (.clk(clock_1_out), .D(or_1_out), .Q(out_3), .reset(Clear));  // open: Qn, preset, en
  D_Flip_Flop d_ff_2 (.clk(clock_1_out), .D(or_2_out), .Q(out_4), .reset(Clear));  // open: Qn, preset, en
  or or_2 (or_2_out, out_3, Data);
  or or_3 (or_3_out, out_4, Data);
  D_Flip_Flop d_ff_3 (.clk(clock_1_out), .D(or_3_out), .Q(out_5), .reset(Clear));  // open: Qn, preset, en
  or or_4 (or_4_out, out_5, Data);
  D_Flip_Flop d_ff_4 (.clk(clock_1_out), .D(or_4_out), .Q(out_6), .reset(Clear));  // open: Qn, preset, en
  D_Flip_Flop d_ff_5 (.clk(clock_1_out), .D(or_5_out), .Q(out_7), .reset(Clear));  // open: Qn, preset, en
  or or_5 (or_5_out, out_6, Data);
endmodule

module Exemplo0067 (
  input  Data,
  input  Clear,
  output out_3,
  output out_4,
  output out_5,
  output out_6,
  output out_7
);

  wire clock_1_out, d_ff_5_qn, or_1_out, or_2_out, or_3_out, or_4_out, or_5_out;

  Clock clock_1 (.out(clock_1_out));
  or or_1 (or_1_out, d_ff_5_qn, Data);
  D_Flip_Flop d_ff_1 (.clk(clock_1_out), .D(or_1_out), .Q(out_3), .reset(Clear));  // open: Qn, preset, en
  D_Flip_Flop d_ff_2 (.clk(clock_1_out), .D(or_2_out), .Q(out_4), .reset(Clear));  // open: Qn, preset, en
  or or_2 (or_2_out, out_3, Data);
  or or_3 (or_3_out, out_4, Data);
  D_Flip_Flop d_ff_3 (.clk(clock_1_out), .D(or_3_out), .Q(out_5), .reset(Clear));  // open: Qn, preset, en
  or or_4 (or_4_out, out_5, Data);
  D_Flip_Flop d_ff_4 (.clk(clock_1_out), .D(or_4_out), .Q(out_6), .reset(Clear));  // open: Qn, preset, en
  D_Flip_Flop d_ff_5 (.clk(clock_1_out), .D(or_5_out), .Q(out_7), .Qn(d_ff_5_qn), .reset(Clear));  // open: preset, en
  or or_5 (or_5_out, out_6, Data);
endmodule
