// Logisim project Exercicio04.circ as structural Verilog: 1 circuit, main circuit main
module main (
  input  CLK,
  input  Data,
  input  CLR,
  output out_4,
  output out_5,
  output out_6,
  output out_7,
  output out_8
);

  wire or_1_out;

  D_Flip_Flop d_ff_1 (.clk(CLK), .D(out_5), .Q(out_4), .reset(CLR));  // open: Qn, preset, en
  or or_1 (or_1_out, out_4, Data);
  D_Flip_Flop d_ff_2 (.clk(CLK), .D(out_6), .Q(out_5), .reset(CLR));  // open: Qn, preset, en
  D_Flip_Flop d_ff_3 (.clk(CLK), .D(out_7), .Q(out_6), .reset(CLR));  // open: Qn, preset, en
  D_Flip_Flop d_ff_4 (.clk(CLK), .D(out_8), .Q(out_7), .reset(CLR));  // open: Qn, preset, en
  D_Flip_Flop d_ff_5 (.clk(CLK), .D(or_1_out), .Q(out_8), .reset(CLR));  // open: Qn, preset, en
endmodule
