// Logisim project Exercicio05.circ as structural Verilog: 1 circuit, main circuit main
module main (
  input  CLK,
  input  CLR,
  input  Data,
  input  in_4,
  input  in_5,
  input  in_6,
  input  in_7,
  input  in_8,
  output out_9,
  output out_10,
  output out_11,
  output out_12,
  output out_13
);

  wire and_1_out, and_2_out, and_3_out, and_4_out, and_5_out;

  D_Flip_Flop d_ff_1 (.clk(CLK), .D(1'b0), .Q(out_9), .preset(and_1_out), .reset(CLR));  // open: Qn, en
  and and_1 (and_1_out, Data, in_4);
  and and_2 (and_2_out, Data, in_5);
  D_Flip_Flop d_ff_2 (.clk(CLK), .D(out_9), .Q(out_10), .preset(and_2_out), .reset(CLR));  // open: Qn, en
  and and_3 (and_3_out, Data, in_6);
  D_Flip_Flop d_ff_3 (.clk(CLK), .D(out_10), .Q(out_11), .preset(and_3_out), .reset(CLR));  // open: Qn, en
  and and_4 (and_4_out, Data, in_7);
  D_Flip_Flop d_ff_4 (.clk(CLK), .D(out_11), .Q(out_12), .preset(and_4_out), .reset(CLR));  // open: Qn, en
  and and_5 (and_5_out, Data, in_8);
  D_Flip_Flop d_ff_5 (.clk(CLK), .D(out_12), .Q(out_13), .preset(and_5_out), .reset(CLR));  // open: Qn, en
endmodule
