// Logisim project Exercicio03.circ as structural Verilog: 1 circuit, main circuit main
module main (
  input  _1,
  input  Pulse,
  output a,
  output b,
  output c,
  output d,
  output e
);

  wire And01_out, not04_out, Not_01_out, Not_02_out, Not_03_out, or01_out, t_ff_1_qn, t_ff_2_qn, t_ff_3_qn,
       t_ff_4_qn, t_ff_5_qn;

  not not04 (not04_out, _1);
  and And01 (And01_out, Not_01_out, t_ff_2_qn, Not_02_out, t_ff_4_qn, Not_03_out);
  T_Flip_Flop t_ff_1 (.clk(_1), .T(_1), .Q(e), .Qn(t_ff_1_qn), .preset(or01_out));  // open: reset, en
  or or01 (or01_out, not04_out, And01_out);
  not Not_01 (Not_01_out, t_ff_1_qn);
  not Not_02 (Not_02_out, t_ff_3_qn);
  not Not_03 (Not_03_out, t_ff_5_qn);
  T_Flip_Flop t_ff_2 (.clk(_1), .T(_1), .Q(d), .Qn(t_ff_2_qn), .preset(or01_out));  // open: reset, en
  T_Flip_Flop t_ff_3 (.clk(_1), .T(_1), .Q(c), .Qn(t_ff_3_qn), .preset(or01_out));  // open: reset, en
  T_Flip_Flop t_ff_4 (.clk(_1), .T(_1), .Q(b), .Qn(t_ff_4_qn), .preset(or01_out));  // open: reset, en
  T_Flip_Flop t_ff_5 (.clk(_1), .T(_1), .Q(a), .Qn(t_ff_5_qn), .preset(or01_out));  // open: reset, en

  // Notes on the sheet:
  //   Nome: Jorge Luis - Contador Decádico Decrescente
endmodule
