// Logisim project Exercicio04.circ as structural Verilog: 1 circuit, main circuit main
module main (
  input  _1,
  input  Pulse,
  input  CLR,
  output a,
  output b,
  output c,
  output d,
  output e
);

  wire And01_out, Nand01_out, not_1_out, not_2_out, not_3_out, t_ff_1_qn, t_ff_2_qn, t_ff_3_qn, t_ff_4_qn;

  nand Nand01 (Nand01_out, not_1_out, d, not_2_out, b, not_3_out);
  T_Flip_Flop t_ff_1 (.clk(_1), .T(_1), .Q(e), .Qn(t_ff_1_qn), .reset(And01_out));  // open: preset, en
  nand And01 (And01_out, CLR, Nand01_out);
  not not_1 (not_1_out, e);
  not not_2 (not_2_out, c);
  not not_3 (not_3_out, a);
  T_Flip_Flop t_ff_2 (.clk(_1), .T(_1), .Q(d), .Qn(t_ff_2_qn), .reset(And01_out));  // open: preset, en
  T_Flip_Flop t_ff_3 (.clk(_1), .T(_1), .Q(c), .Qn(t_ff_3_qn), .reset(And01_out));  // open: preset, en
  T_Flip_Flop t_ff_4 (.clk(_1), .T(_1), .Q(b), .Qn(t_ff_4_qn), .reset(And01_out));  // open: preset, en
  T_Flip_Flop t_ff_5 (.clk(_1), .T(_1), .Q(a), .reset(And01_out));  // open: Qn, preset, en

  // Notes on the sheet:
  //   Nome: Jorge Luis - Contador Decádico Crescente
endmodule
