// Logisim project Exercicio05.circ as structural Verilog: 1 circuit, main circuit main
module main (
  input  Pulso,
  input  CLR,
  output a,
  output b,
  output c
);

  wire And01_out, j_k_ff_2_qn, j_k_ff_3_qn, Not01_out, Or01_out;

  or Or01 (Or01_out, CLR, And01_out);
  and And01 (And01_out, a, b, Not01_out);
  J_K_Flip_Flop j_k_ff_1 (.J(j_k_ff_2_qn), .K(j_k_ff_2_qn), .Q(a), .reset(Or01_out));  // open: clk, Qn, preset, en
  J_K_Flip_Flop j_k_ff_2 (
    .J(j_k_ff_3_qn), .K(j_k_ff_3_qn), .Q(b), .Qn(j_k_ff_2_qn), .reset(Or01_out));  // open: clk, preset, en
  not Not01 (Not01_out, c);
  J_K_Flip_Flop j_k_ff_3 (.J(Pulso), .K(Pulso), .Q(c), .Qn(j_k_ff_3_qn), .reset(Or01_out));  // open: clk, preset, en

  // Notes on the sheet:
  //   Nome: Jorge Luis - Contador Assincrono Modulo 6
endmodule
