// Logisim project Extra02.circ as structural Verilog: 1 circuit, main circuit main
module main (
  input  Input,
  input  Clear,
  output a,
  output b,
  output c
);

  wire Clock_out, j_k_ff_3_qn, or_1_out;

  Clock Clock (.out(Clock_out));
  J_K_Flip_Flop j_k_ff_1 (.J(Clock_out), .K(or_1_out), .Q(a), .reset(Clear));  // open: clk, Qn, preset, en
  or or_1 (or_1_out, j_k_ff_3_qn, Input);
  J_K_Flip_Flop j_k_ff_2 (.J(Clock_out), .K(a), .Q(b), .reset(Clear));  // open: clk, Qn, preset, en
  J_K_Flip_Flop j_k_ff_3 (.J(Clock_out), .K(b), .Q(c), .Qn(j_k_ff_3_qn), .reset(Clear));  // open: clk, preset, en

  // Notes on the sheet:
  //   Nome: Jorge Luis - Contador em Anel Torcido
endmodule
