// Logisim project (Down) Asynchronous counter.circ as structural Verilog: 1 circuit, main circuit main
module main (
  input  pulse,
  input  _1,
  input  clr,
  output a,
  output b,
  output c,
  output d
);

  J_K_Flip_Flop j_k_ff_1 (.J(_1), .clk(b), .K(_1), .Qn(a), .reset(clr));  // open: Q, preset, en
  J_K_Flip_Flop j_k_ff_2 (.J(_1), .clk(c), .K(_1), .Qn(b), .reset(clr));  // open: Q, preset, en
  J_K_Flip_Flop j_k_ff_3 (.J(_1), .clk(d), .K(_1), .Qn(c), .reset(clr));  // open: Q, preset, en
  J_K_Flip_Flop j_k_ff_4 (.J(_1), .clk(pulse), .K(_1), .Qn(d), .reset(clr));  // open: Q, preset, en

  // Notes on the sheet:
  //   (Down) Asynchronous counter
endmodule
