// Logisim project (Down) Decade counter.circ as structural Verilog: 1 circuit, main circuit main
module main (
  input  _1,
  input  pulse,
  output a,
  output b,
  output c,
  output d
);

  wire and_1_out, j_k_ff_1_qn, j_k_ff_2_qn, j_k_ff_3_qn, j_k_ff_4_qn, not_1_out, not_2_out, not_3_out,
       or_1_out;

  not not_1 (not_1_out, _1);
  and and_1 (and_1_out, not_2_out, j_k_ff_2_qn, not_3_out, j_k_ff_4_qn);
  J_K_Flip_Flop j_k_ff_1 (.J(_1), .clk(pulse), .K(_1), .Q(d), .Qn(j_k_ff_1_qn), .preset(or_1_out));  // open: en, reset
  or or_1 (or_1_out, not_1_out, and_1_out);
  not not_2 (not_2_out, j_k_ff_1_qn);
  not not_3 (not_3_out, j_k_ff_3_qn);
  J_K_Flip_Flop j_k_ff_2 (.J(_1), .clk(d), .K(_1), .Q(c), .Qn(j_k_ff_2_qn), .preset(or_1_out));  // open: en, reset
  J_K_Flip_Flop j_k_ff_3 (.J(_1), .clk(c), .K(_1), .Q(b), .Qn(j_k_ff_3_qn), .preset(or_1_out));  // open: en, reset
  J_K_Flip_Flop j_k_ff_4 (.J(_1), .clk(b), .K(_1), .Q(a), .Qn(j_k_ff_4_qn), .preset(or_1_out));  // open: en, reset

  // Notes on the sheet:
  //   (Down) Decade counter
endmodule
