// Logisim project (Up) Asynchronous counter.circ as structural Verilog: 1 circuit, main circuit main
module main (
  input  pulse,
  input  _1,
  input  clr,
  output a,
  output b,
  output c,
  output d
);

  wire j_k_ff_2_q, j_k_ff_3_q, j_k_ff_4_q;

  J_K_Flip_Flop j_k_ff_1 (.J(_1), .clk(j_k_ff_2_q), .K(_1), .Qn(a), .reset(clr));  // open: Q, preset, en
  J_K_Flip_Flop j_k_ff_2 (.J(_1), .clk(j_k_ff_3_q), .K(_1), .Q(j_k_ff_2_q), .Qn(b), .reset(clr));  // open: preset, en
  J_K_Flip_Flop j_k_ff_3 (.J(_1), .clk(j_k_ff_4_q), .K(_1), .Q(j_k_ff_3_q), .Qn(c), .reset(clr));  // open: preset, en
  J_K_Flip_Flop j_k_ff_4 (.J(_1), .clk(pulse), .K(_1), .Q(j_k_ff_4_q), .Qn(d), .reset(clr));  // open: preset, en

  // Notes on the sheet:
  //   (Up) Asynchronous counter
endmodule
