// Logisim project Exercicio02.circ as structural Verilog: 1 circuit, main circuit main
module main (
  input  in_1,
  input  in_2,
  output out_3,
  output out_4,
  output out_5,
  output out_6,
  output out_7
);

  wire t_ff_2_q, t_ff_3_q, t_ff_5_q;

  Clock clock_1 (.out(in_1));
  T_Flip_Flop t_ff_1 (.clk(t_ff_2_q), .T(in_1), .Qn(out_3), .reset(in_2));  // open: Q, preset, en
  T_Flip_Flop t_ff_2 (.clk(t_ff_3_q), .T(in_1), .Q(t_ff_2_q), .Qn(out_4), .reset(in_2));  // open: preset, en
  T_Flip_Flop t_ff_3 (.clk(in_1), .T(in_1), .Q(t_ff_3_q), .Qn(out_5), .reset(in_2));  // open: preset, en
  T_Flip_Flop t_ff_4 (.clk(t_ff_5_q), .T(in_1), .Q(in_1), .Qn(out_6), .reset(in_2));  // open: preset, en
  T_Flip_Flop t_ff_5 (.clk(in_1), .T(in_1), .Q(t_ff_5_q), .Qn(out_7), .reset(in_2));  // open: preset, en

  // Notes on the sheet:
  //   Contador Assíncrono Crescente
endmodule
