// Logisim project Exercicio04.circ as structural Verilog: 1 circuit, main circuit main
module main (
  input  in_1,
  input  in_2,
  output out_3,
  output out_4,
  output out_5,
  output out_6,
  output out_7
);

  wire and_1_out, and_2_out, clock_1_out, not_1_out, not_2_out, t_ff_1_qn, t_ff_2_qn, t_ff_3_qn, t_ff_4_qn;

  Clock clock_1 (.out(clock_1_out));
  and and_1 (and_1_out, not_1_out, out_6, out_3, not_2_out, out_3);
  T_Flip_Flop t_ff_1 (.clk(clock_1_out), .T(in_1), .Q(out_4), .Qn(t_ff_1_qn), .reset(and_2_out));  // open: preset, en
  and and_2 (and_2_out, in_2, and_1_out);
  not not_1 (not_1_out, out_4);
  not not_2 (not_2_out, out_4);
  T_Flip_Flop t_ff_2 (.clk(t_ff_1_qn), .T(in_1), .Q(out_6), .Qn(t_ff_2_qn), .reset(and_2_out));  // open: preset, en
  T_Flip_Flop t_ff_3 (.clk(t_ff_2_qn), .Q(out_3), .Qn(t_ff_3_qn), .reset(and_2_out));  // open: T, preset, en
  T_Flip_Flop t_ff_4 (.clk(t_ff_3_qn), .Q(out_4), .Qn(t_ff_4_qn), .reset(and_2_out));  // open: T, preset, en
  T_Flip_Flop t_ff_5 (.clk(t_ff_4_qn), .T(in_1), .Q(out_3), .reset(and_2_out));  // open: Qn, preset, en

  assign out_5 = out_3;
  assign out_7 = out_4;

  // Notes on the sheet:
  //   Contador Decádico Crescente
endmodule
