// Logisim project Exercicio01.circ as structural Verilog: 1 circuit, main circuit main
module main (
  input  Pulse,
  input  _1,
  input  Clk,
  output A,
  output B,
  output C,
  output D,
  output E
);

  T_Flip_Flop t_ff_1 (.clk(_1), .T(_1), .Qn(A), .reset(Clk));  // open: Q, preset, en
  T_Flip_Flop t_ff_2 (.clk(_1), .T(_1), .Qn(B), .reset(Clk));  // open: Q, preset, en
  T_Flip_Flop t_ff_3 (.clk(_1), .T(_1), .Qn(C), .reset(Clk));  // open: Q, preset, en
  T_Flip_Flop t_ff_4 (.clk(_1), .T(_1), .Qn(D), .reset(Clk));  // open: Q, preset, en
  T_Flip_Flop t_ff_5 (.clk(_1), .T(_1), .Qn(E), .reset(Clk));  // open: Q, preset, en

  // Notes on the sheet:
  //   Nome: Jorge Luis - Contador Assincrono Decrescente
endmodule
