// Logisim project Exercicio02.circ as structural Verilog: 1 circuit, main circuit main
module main (
  input  Pulse,
  input  _1,
  input  Clk,
  output A,
  output B,
  output C,
  output D,
  output E
);

  wire t_ff_2_q, t_ff_3_q, t_ff_4_q, t_ff_5_q;

  T_Flip_Flop t_ff_1 (.clk(_1), .T(_1), .Qn(A), .reset(Clk));  // open: Q, preset, en
  T_Flip_Flop t_ff_2 (.clk(_1), .T(_1), .Q(t_ff_2_q), .Qn(B), .reset(Clk));  // open: preset, en
  T_Flip_Flop t_ff_3 (.clk(_1), .T(_1), .Q(t_ff_3_q), .Qn(C), .reset(Clk));  // open: preset, en
  T_Flip_Flop t_ff_4 (.clk(_1), .T(_1), .Q(t_ff_4_q), .Qn(D), .reset(Clk));  // open: preset, en
  T_Flip_Flop t_ff_5 (.clk(_1), .T(_1), .Q(t_ff_5_q), .Qn(E), .reset(Clk));  // open: preset, en

  // Notes on the sheet:
  //   Nome: Jorge Luis - Contador Assincrono Crescente
endmodule
