// Logisim project cir 1.circ as structural Verilog: 1 circuit, main circuit main
module main (
  input  pulso,
  input  clear,
  input  pulso_2,
  input  clear_2,
  output out_5,
  output out_6,
  output out_7,
  output out_8,
  output out_9,
  output out_10
);

  wire and_1_out, and_2_out, and_3_out, and_4_out, and_5_out, j_k_ff_3_qn, j_k_ff_4_qn, j_k_ff_5_qn,
       j_k_ff_6_qn, not_1_out, not_2_out, not_3_out, not_4_out, not_5_out, or_1_out, or_2_out, or_3_out,
       or_4_out, or_5_out;

  not not_1 (not_1_out, or_1_out);
  or or_1 (or_1_out, clear, and_1_out);
  and and_1 (and_1_out, out_5, out_6, not_4_out);
  or or_2 (or_2_out, clear_2, and_3_out);
  and and_2 (and_2_out, not_1_out, j_k_ff_3_qn);
  J_K_Flip_Flop j_k_ff_1 (.J(and_2_out), .clk(or_3_out), .K(or_3_out), .Q(out_5));  // open: Qn, preset, en, reset
  or or_3 (or_3_out, j_k_ff_3_qn, or_1_out);
  J_K_Flip_Flop j_k_ff_2 (
    .J(j_k_ff_4_qn), .clk(j_k_ff_4_qn), .K(j_k_ff_4_qn), .Q(out_8), .reset(or_2_out));  // open: Qn, preset, en
  and and_3 (and_3_out, out_8, not_2_out, out_10);
  not not_2 (not_2_out, out_9);
  and and_4 (and_4_out, j_k_ff_6_qn, not_3_out);
  not not_3 (not_3_out, or_1_out);
  or or_4 (or_4_out, j_k_ff_6_qn, or_1_out);
  not not_4 (not_4_out, out_7);
  not not_5 (not_5_out, or_1_out);
  J_K_Flip_Flop j_k_ff_3 (
    .J(and_4_out), .clk(or_4_out), .K(or_4_out), .Q(out_6), .Qn(j_k_ff_3_qn));  // open: preset, en, reset
  J_K_Flip_Flop j_k_ff_4 (
    .J(j_k_ff_5_qn), .clk(j_k_ff_5_qn), .K(j_k_ff_5_qn), .Q(out_9), .Qn(j_k_ff_4_qn), .reset(or_2_out));  // open: preset, en
  and and_5 (and_5_out, not_5_out, pulso);
  or or_5 (or_5_out, pulso, or_1_out);
  J_K_Flip_Flop j_k_ff_5 (
    .J(pulso_2), .clk(pulso_2), .K(pulso_2), .Q(out_10), .Qn(j_k_ff_5_qn), .reset(or_2_out));  // open: preset, en
  J_K_Flip_Flop j_k_ff_6 (
    .J(and_5_out), .clk(or_5_out), .K(or_5_out), .Q(out_7), .Qn(j_k_ff_6_qn));  // open: preset, en, reset

  // Notes on the sheet:
  //   MODULO 6 = [0:5]  // ESTA' PERTO DA SOLUCAO!
endmodule
