// Logisim project Exercicio0001.circ as structural Verilog: 1 circuit, main circuit main
module main (
  input  in_1,
  input  in_2,
  output out_3,
  output out_4,
  output out_5,
  output out_6
);

  wire clock_1_out;

  T_Flip_Flop t_ff_1 (.clk(out_4), .T(in_1), .Q(out_3), .reset(in_2));  // open: Qn, preset, en
  T_Flip_Flop t_ff_2 (.clk(out_5), .T(in_1), .Q(out_4), .reset(in_2));  // open: Qn, preset, en
  T_Flip_Flop t_ff_3 (.clk(out_6), .T(in_1), .Q(out_5), .reset(in_2));  // open: Qn, preset, en
  Clock clock_1 (.out(clock_1_out));
  T_Flip_Flop t_ff_4 (.clk(clock_1_out), .T(in_1), .Q(out_6), .reset(in_2));  // open: Qn, preset, en
endmodule
