// Logisim project Exercicio0004.circ as structural Verilog: 1 circuit, main circuit main
module main (
  input  in_1,
  input  in_2,
  output out_3,
  output out_4,
  output out_5,
  output out_6
);

  wire clock_1_out, nand_1_out, nand_2_out, not_1_out, not_2_out, t_ff_1_qn, t_ff_2_qn, t_ff_3_qn;

  Clock clock_1 (.out(clock_1_out));
  nand nand_1 (nand_1_out, not_1_out, out_5, not_2_out, out_3);
  nand nand_2 (nand_2_out, in_2, nand_1_out);
  not not_1 (not_1_out, out_6);
  not not_2 (not_2_out, out_4);
  T_Flip_Flop t_ff_1 (.clk(clock_1_out), .T(in_1), .Q(out_6), .Qn(t_ff_1_qn), .reset(nand_2_out));  // open: preset, en
  T_Flip_Flop t_ff_2 (.clk(t_ff_1_qn), .T(in_1), .Q(out_5), .Qn(t_ff_2_qn), .reset(nand_2_out));  // open: preset, en
  T_Flip_Flop t_ff_3 (.clk(t_ff_2_qn), .T(in_1), .Q(out_4), .Qn(t_ff_3_qn), .reset(nand_2_out));  // open: preset, en
  T_Flip_Flop t_ff_4 (.clk(t_ff_3_qn), .T(in_1), .Q(out_3), .reset(nand_2_out));  // open: Qn, preset, en
endmodule
