// Logisim project Exercicio0005.circ as structural Verilog: 1 circuit, main circuit main
module main (
  input  in_1,
  input  in_2,
  output out_3,
  output out_4,
  output out_5
);

  wire clock_1_out, j_k_ff_2_q, j_k_ff_3_q, nand_1_out;

  J_K_Flip_Flop j_k_ff_1 (.J(1'b1), .clk(j_k_ff_2_q), .K(1'b1), .Qn(out_3), .reset(nand_1_out));  // open: Q, preset, en
  nand nand_1 (nand_1_out, in_1, in_2);
  J_K_Flip_Flop j_k_ff_2 (
    .J(1'b1), .clk(j_k_ff_3_q), .K(1'b1), .Q(j_k_ff_2_q), .Qn(out_4), .reset(nand_1_out));  // open: preset, en
  J_K_Flip_Flop j_k_ff_3 (
    .J(1'b1), .clk(clock_1_out), .K(1'b1), .Q(j_k_ff_3_q), .Qn(out_5), .reset(nand_1_out));  // open: preset, en
  Clock clock_1 (.out(clock_1_out));
endmodule
