// Logisim project guia9.circ as structural Verilog: 5 circuits, main circuit c1
module c1 (
  input  in_1,
  input  in_2,
  output out_3,
  output out_4,
  output out_5,
  output out_6
);

  wire clock_1_out;

  T_Flip_Flop t_ff_1 (.clk(out_4), .T(in_2), .Q(out_3), .reset(in_1));  // open: Qn, preset, en
  T_Flip_Flop t_ff_2 (.clk(out_5), .T(in_2), .Q(out_4), .reset(in_1));  // open: Qn, preset, en
  T_Flip_Flop t_ff_3 (.clk(out_6), .T(in_2), .Q(out_5), .reset(in_1));  // open: Qn, preset, en
  T_Flip_Flop t_ff_4 (.clk(clock_1_out), .T(in_2), .Q(out_6), .reset(in_1));  // open: Qn, preset, en
  Clock clock_1 (.out(clock_1_out));
endmodule

module c2 (
  input  in_1,
  input  in_2,
  output out_3,
  output out_4,
  output out_5,
  output out_6
);

  wire clock_1_out, t_ff_2_q, t_ff_3_q, t_ff_4_q;

  Clock clock_1 (.out(clock_1_out));
  T_Flip_Flop t_ff_1 (.clk(t_ff_2_q), .T(in_2), .Qn(out_3), .reset(in_1));  // open: Q, preset, en
  T_Flip_Flop t_ff_2 (.clk(t_ff_3_q), .T(in_2), .Q(t_ff_2_q), .Qn(out_4), .reset(in_1));  // open: preset, en
  T_Flip_Flop t_ff_3 (.clk(t_ff_4_q), .T(in_2), .Q(t_ff_3_q), .Qn(out_5), .reset(in_1));  // open: preset, en
  T_Flip_Flop t_ff_4 (.clk(clock_1_out), .T(in_2), .Q(t_ff_4_q), .Qn(out_6), .reset(in_1));  // open: preset, en
endmodule

module c3 (
  input  in_1,
  output out_2,
  output out_3,
  output out_4,
  output out_5
);

  wire and_1_out, clock_1_out, not_1_out, not_2_out, not_3_out, or_1_out, t_ff_1_qn, t_ff_2_qn, t_ff_3_qn,
       t_ff_4_qn;

  not not_1 (not_1_out, in_1);
  and and_1 (and_1_out, not_2_out, t_ff_2_qn, not_3_out, t_ff_4_qn);
  Clock clock_1 (.out(clock_1_out));
  or or_1 (or_1_out, not_1_out, and_1_out);
  not not_2 (not_2_out, t_ff_1_qn);
  not not_3 (not_3_out, t_ff_3_qn);
  T_Flip_Flop t_ff_1 (.clk(clock_1_out), .T(in_1), .Q(out_5), .Qn(t_ff_1_qn), .preset(or_1_out));  // open: reset, en
  T_Flip_Flop t_ff_2 (.clk(out_5), .T(in_1), .Q(out_4), .Qn(t_ff_2_qn), .preset(or_1_out));  // open: reset, en
  T_Flip_Flop t_ff_3 (.clk(out_4), .T(in_1), .Q(out_3), .Qn(t_ff_3_qn), .preset(or_1_out));  // open: reset, en
  T_Flip_Flop t_ff_4 (.clk(out_3), .T(in_1), .Q(out_2), .Qn(t_ff_4_qn), .preset(or_1_out));  // open: reset, en
endmodule

module c4 (
  input  in_1,
  input  in_2,
  output out_3,
  output out_4,
  output out_5,
  output out_6
);

  wire clock_1_out, nand_1_out, nand_2_out, not_1_out, not_2_out, t_ff_1_qn, t_ff_2_qn, t_ff_3_qn;

  nand nand_1 (nand_1_out, not_1_out, out_5, not_2_out, out_3);
  Clock clock_1 (.out(clock_1_out));
  nand nand_2 (nand_2_out, in_2, nand_1_out);
  not not_1 (not_1_out, out_6);
  not not_2 (not_2_out, out_4);
  T_Flip_Flop t_ff_1 (.clk(clock_1_out), .T(in_1), .Q(out_6), .Qn(t_ff_1_qn), .reset(nand_2_out));  // open: preset, en
  T_Flip_Flop t_ff_2 (.clk(t_ff_1_qn), .T(in_1), .Q(out_5), .Qn(t_ff_2_qn), .reset(nand_2_out));  // open: preset, en
  T_Flip_Flop t_ff_3 (.clk(t_ff_2_qn), .T(in_1), .Q(out_4), .Qn(t_ff_3_qn), .reset(nand_2_out));  // open: preset, en
  T_Flip_Flop t_ff_4 (.clk(t_ff_3_qn), .T(in_1), .Q(out_3), .reset(nand_2_out));  // open: Qn, preset, en
endmodule

module c5 (
  input  in_1,
  input  in_2,
  input  in_3,
  output out_4,
  output out_5,
  output out_6
);

  wire clock_1_out, j_k_ff_2_q, j_k_ff_3_q, nand_1_out;

  J_K_Flip_Flop j_k_ff_1 (.J(in_1), .clk(j_k_ff_2_q), .K(in_1), .Qn(out_4), .reset(nand_1_out));  // open: Q, preset, en
  nand nand_1 (nand_1_out, in_2, in_3);
  J_K_Flip_Flop j_k_ff_2 (
    .J(in_1), .clk(j_k_ff_3_q), .K(in_1), .Q(j_k_ff_2_q), .Qn(out_5), .reset(nand_1_out));  // open: preset, en
  J_K_Flip_Flop j_k_ff_3 (
    .J(in_1), .clk(clock_1_out), .K(in_1), .Q(j_k_ff_3_q), .Qn(out_6), .reset(nand_1_out));  // open: preset, en
  Clock clock_1 (.out(clock_1_out));
endmodule
