// Logisim project Guia09.circ as structural Verilog: 5 circuits, main circuit Exemplo01
module Exemplo01 (
  input  Input,
  input  Clear,
  output out_3,
  output out_4,
  output out_5,
  output out_6
);

  wire Clock_out;

  Clock Clock (.out(Clock_out));
  J_K_Flip_Flop j_k_ff_1 (.J(Input), .clk(out_4), .K(Input), .Qn(out_3), .reset(Clear));  // open: Q, preset, en
  J_K_Flip_Flop j_k_ff_2 (.J(Input), .clk(out_5), .K(Input), .Qn(out_4), .reset(Clear));  // open: Q, preset, en
  J_K_Flip_Flop j_k_ff_3 (.J(Input), .clk(out_6), .K(Input), .Qn(out_5), .reset(Clear));  // open: Q, preset, en
  J_K_Flip_Flop j_k_ff_4 (.J(Input), .clk(Clock_out), .K(Input), .Qn(out_6), .reset(Clear));  // open: Q, preset, en
endmodule

module Exemplo02 (
  input  Input,
  input  Clear,
  output out_3,
  output out_4,
  output out_5,
  output out_6
);

  wire Clock_out, j_k_ff_2_qn, j_k_ff_3_qn, j_k_ff_4_qn;

  Clock Clock (.out(Clock_out));
  J_K_Flip_Flop j_k_ff_1 (.J(Input), .clk(j_k_ff_2_qn), .K(Input), .Q(out_3), .reset(Clear));  // open: Qn, preset, en
  J_K_Flip_Flop j_k_ff_2 (
    .J(Input), .clk(j_k_ff_3_qn), .K(Input), .Q(out_4), .Qn(j_k_ff_2_qn), .reset(Clear));  // open: preset, en
  J_K_Flip_Flop j_k_ff_3 (
    .J(Input), .clk(j_k_ff_4_qn), .K(Input), .Q(out_5), .Qn(j_k_ff_3_qn), .reset(Clear));  // open: preset, en
  J_K_Flip_Flop j_k_ff_4 (
    .J(Input), .clk(Clock_out), .K(Input), .Q(out_6), .Qn(j_k_ff_4_qn), .reset(Clear));  // open: preset, en
endmodule

module Exemplo03 (
  input  Input,
  output out_2,
  output out_3,
  output out_4,
  output out_5
);

  wire and_1_out, Clock_out, not_1_out, not_2_out, not_3_out, or_1_out, t_ff_1_qn, t_ff_2_qn, t_ff_3_qn,
       t_ff_4_qn;

  Clock Clock (.out(Clock_out));
  not not_1 (not_1_out, Input);
  and and_1 (and_1_out, t_ff_1_qn, not_2_out, not_3_out, t_ff_4_qn);
  or or_1 (or_1_out, not_1_out, and_1_out);
  not not_2 (not_2_out, t_ff_2_qn);
  not not_3 (not_3_out, t_ff_3_qn);
  T_Flip_Flop t_ff_1 (.clk(out_3), .T(Input), .Q(out_2), .Qn(t_ff_1_qn), .reset(or_1_out));  // open: preset, en
  T_Flip_Flop t_ff_2 (.clk(out_4), .T(Input), .Q(out_3), .Qn(t_ff_2_qn), .reset(or_1_out));  // open: preset, en
  T_Flip_Flop t_ff_3 (.clk(out_5), .T(Input), .Q(out_4), .Qn(t_ff_3_qn), .reset(or_1_out));  // open: preset, en
  T_Flip_Flop t_ff_4 (.clk(Clock_out), .T(Input), .Q(out_5), .Qn(t_ff_4_qn), .reset(or_1_out));  // open: preset, en
endmodule

module Exemplo04 (
  input  Input,
  output out_2,
  output out_3,
  output out_4,
  output out_5
);

  wire and_1_out, Clock_out, not_1_out, not_2_out, not_3_out, or_1_out, t_ff_2_qn, t_ff_3_qn, t_ff_4_qn;

  Clock Clock (.out(Clock_out));
  not not_1 (not_1_out, Input);
  and and_1 (and_1_out, out_2, not_2_out, out_4, not_3_out);
  or or_1 (or_1_out, not_1_out, and_1_out);
  not not_2 (not_2_out, out_3);
  not not_3 (not_3_out, out_5);
  T_Flip_Flop t_ff_1 (.clk(t_ff_2_qn), .T(Input), .Q(out_2), .reset(or_1_out));  // open: Qn, preset, en
  T_Flip_Flop t_ff_2 (.clk(t_ff_3_qn), .T(Input), .Q(out_3), .Qn(t_ff_2_qn), .reset(or_1_out));  // open: preset, en
  T_Flip_Flop t_ff_3 (.clk(t_ff_4_qn), .T(Input), .Q(out_4), .Qn(t_ff_3_qn), .reset(or_1_out));  // open: preset, en
  T_Flip_Flop t_ff_4 (.clk(Clock_out), .T(Input), .Q(out_5), .Qn(t_ff_4_qn), .reset(or_1_out));  // open: preset, en
endmodule

module Exemplo05 (
  input  in_1,
  output out_2,
  output out_3,
  output out_4
);

  wire and_1_out, Input_out, j_k_ff_2_qn, j_k_ff_3_qn, not_1_out, or_1_out;

  Clock Input (.out(Input_out));
  and and_1 (and_1_out, out_2, out_3, not_1_out);
  J_K_Flip_Flop j_k_ff_1 (
    .J(j_k_ff_2_qn), .clk(j_k_ff_2_qn), .K(j_k_ff_2_qn), .Q(out_2), .reset(or_1_out));  // open: Qn, preset, en
  or or_1 (or_1_out, in_1, and_1_out);
  not not_1 (not_1_out, out_4);
  J_K_Flip_Flop j_k_ff_2 (
    .J(j_k_ff_3_qn), .clk(j_k_ff_3_qn), .K(j_k_ff_3_qn), .Q(out_3), .Qn(j_k_ff_2_qn), .reset(or_1_out));  // open: preset, en
  J_K_Flip_Flop j_k_ff_3 (
    .J(Input_out), .clk(Input_out), .K(Input_out), .Q(out_4), .Qn(j_k_ff_3_qn), .reset(or_1_out));  // open: preset, en
endmodule
