// Logisim project Exercicio01.circ as structural Verilog: 1 circuit, main circuit main
module main (
  input  in_1,
  input  in_2,
  output out_3,
  output out_4,
  output out_5,
  output out_6,
  output out_7
);

  wire clock_1_out;

  Clock clock_1 (.out(clock_1_out));
  T_Flip_Flop t_ff_1 (.clk(out_4), .T(in_1), .Qn(out_3), .reset(in_2));  // open: Q, preset, en
  T_Flip_Flop t_ff_2 (.clk(out_5), .T(in_1), .Qn(out_4), .reset(in_2));  // open: Q, preset, en
  T_Flip_Flop t_ff_3 (.clk(out_6), .T(clock_1_out), .Qn(out_5), .reset(in_2));  // open: Q, preset, en
  T_Flip_Flop t_ff_4 (.clk(out_7), .Qn(out_6), .reset(in_2));  // open: T, Q, preset, en
  T_Flip_Flop t_ff_5 (.clk(clock_1_out), .T(in_1), .Qn(out_7), .reset(in_2));  // open: Q, preset, en

  // Notes on the sheet:
  //   Contador Assíncrono Decrescente
endmodule
