// Logisim project Circuitos.circ as structural Verilog: 6 circuits, main circuit main
module main (
);


  // Notes on the sheet:
  //   Nome: Mateus Augusto Moraes Ferreira     Matricula: 435669
endmodule

module Exemplo0091 (
  input  _1,
  input  CLEAR,
  output out_3,
  output out_4,
  output out_5,
  output out_6,
  output out_7
);

  wire CLK_out;

  Clock CLK (.out(CLK_out));
  T_Flip_Flop _4 (.clk(out_4), .T(_1), .Q(out_3), .reset(CLEAR));  // open: Qn, preset, en
  T_Flip_Flop _3 (.clk(out_5), .T(_1), .Q(out_4), .reset(CLEAR));  // open: Qn, preset, en
  T_Flip_Flop _2 (.clk(out_6), .T(_1), .Q(out_5), .reset(CLEAR));  // open: Qn, preset, en
  T_Flip_Flop u__1 (.clk(out_7), .T(_1), .Q(out_6), .reset(CLEAR));  // open: Qn, preset, en
  T_Flip_Flop _0 (.clk(CLK_out), .T(_1), .Q(out_7), .reset(CLEAR));  // open: Qn, preset, en

  // Notes on the sheet:
  //   Nome: Mateus Augusto Moraes Ferreira     Matricula: 435669
endmodule

module Exemplo0092 (
  input  _1,
  input  CLEAR,
  output out_3,
  output out_4,
  output out_5,
  output out_6,
  output out_7
);

  wire _0_qn, _1_qn, _2_qn, _3_qn, CLK_out;

  Clock CLK (.out(CLK_out));
  T_Flip_Flop _4 (.clk(_3_qn), .T(_1), .Q(out_3), .reset(CLEAR));  // open: Qn, preset, en
  T_Flip_Flop _3 (.clk(_2_qn), .T(_1), .Q(out_4), .Qn(_3_qn), .reset(CLEAR));  // open: preset, en
  T_Flip_Flop _2 (.clk(_1_qn), .T(_1), .Q(out_5), .Qn(_2_qn), .reset(CLEAR));  // open: preset, en
  T_Flip_Flop u__1 (.clk(_0_qn), .T(_1), .Q(out_6), .Qn(_1_qn), .reset(CLEAR));  // open: preset, en
  T_Flip_Flop _0 (.clk(CLK_out), .T(_1), .Q(out_7), .Qn(_0_qn), .reset(CLEAR));  // open: preset, en

  // Notes on the sheet:
  //   Nome: Mateus Augusto Moraes Ferreira     Matricula: 435669
endmodule

module Exemplo0093 (
  input  _1,
  output out_2,
  output out_3,
  output out_4,
  output out_5
);

  wire _0_qn, _1_qn, _2_qn, _3_qn, and_1_out, CLK_out, not_1_out, not_2_out, not_3_out, or_1_out;

  Clock CLK (.out(CLK_out));
  not not_1 (not_1_out, _1);
  or or_1 (or_1_out, not_1_out, and_1_out);
  and and_1 (and_1_out, _3_qn, not_2_out, not_3_out, _0_qn);
  T_Flip_Flop _3 (.clk(out_3), .T(_1), .Q(out_2), .Qn(_3_qn), .reset(or_1_out));  // open: preset, en
  not not_2 (not_2_out, _2_qn);
  not not_3 (not_3_out, _1_qn);
  T_Flip_Flop _2 (.clk(out_4), .T(_1), .Q(out_3), .Qn(_2_qn), .reset(or_1_out));  // open: preset, en
  T_Flip_Flop u__1 (.clk(out_5), .T(_1), .Q(out_4), .Qn(_1_qn), .reset(or_1_out));  // open: preset, en
  T_Flip_Flop _0 (.clk(CLK_out), .T(_1), .Q(out_5), .Qn(_0_qn), .reset(or_1_out));  // open: preset, en

  // Notes on the sheet:
  //   Contador Decrescete de 15 a 7, depois 0.
  //   Nome: Mateus Augusto Moraes Ferreira     Matricula: 435669
endmodule

module Exemplo0094 (
  input  _1,
  output out_2,
  output out_3,
  output out_4,
  output out_5
);

  wire _0_qn, _1_qn, _2_qn, and_1_out, CLK_out, not_1_out, not_2_out, not_3_out, or_1_out;

  Clock CLK (.out(CLK_out));
  not not_1 (not_1_out, _1);
  or or_1 (or_1_out, not_1_out, and_1_out);
  and and_1 (and_1_out, out_2, not_2_out, out_4, not_3_out);
  T_Flip_Flop _3 (.clk(_2_qn), .T(_1), .Q(out_2), .reset(or_1_out));  // open: Qn, preset, en
  not not_2 (not_2_out, out_3);
  not not_3 (not_3_out, out_5);
  T_Flip_Flop _2 (.clk(_1_qn), .T(_1), .Q(out_3), .Qn(_2_qn), .reset(or_1_out));  // open: preset, en
  T_Flip_Flop u__1 (.clk(_0_qn), .T(_1), .Q(out_4), .Qn(_1_qn), .reset(or_1_out));  // open: preset, en
  T_Flip_Flop _0 (.clk(CLK_out), .T(_1), .Q(out_5), .Qn(_0_qn), .reset(or_1_out));  // open: preset, en

  // Notes on the sheet:
  //   Contador Decrescete de 9 a 0
  //   Nome: Mateus Augusto Moraes Ferreira     Matricula: 435669
endmodule

module Exemplo0095 (
  input  CLEAR,
  output out_2,
  output out_3,
  output out_4
);

  wire _0_qn, _1_qn, and_1_out, CLK_out, not_1_out, or_1_out;

  Clock CLK (.out(CLK_out));
  or or_1 (or_1_out, CLEAR, and_1_out);
  and and_1 (and_1_out, out_2, out_3, not_1_out);
  not not_1 (not_1_out, out_4);
  J_K_Flip_Flop _2 (.J(_1_qn), .clk(_1_qn), .K(_1_qn), .Q(out_2), .reset(or_1_out));  // open: Qn, preset, en
  J_K_Flip_Flop _1 (.J(_0_qn), .clk(_0_qn), .K(_0_qn), .Q(out_3), .Qn(_1_qn), .reset(or_1_out));  // open: preset, en
  J_K_Flip_Flop _0 (
    .J(CLK_out), .clk(CLK_out), .K(CLK_out), .Q(out_4), .Qn(_0_qn), .reset(or_1_out));  // open: preset, en

  // Notes on the sheet:
  //   Contador Decrescete de 5 a 0
  //   Nome: Mateus Augusto Moraes Ferreira     Matricula: 435669
endmodule
