// Logisim project guia09.circ as structural Verilog
module Exemplo0071 (
  input  Pulse,
  input  Toggle,
  input  Clear,
  output out_4,
  output out_5,
  output out_6,
  output out_7
);

  T_Flip_Flop t_ff_1 (.clk(out_5), .T(Toggle), .Qn(out_4), .reset(Clear));  // open: Q, preset, en
  T_Flip_Flop t_ff_2 (.clk(out_6), .T(Toggle), .Qn(out_5), .reset(Clear));  // open: Q, preset, en
  T_Flip_Flop t_ff_3 (.clk(out_7), .T(Toggle), .Qn(out_6), .reset(Clear));  // open: Q, preset, en
  T_Flip_Flop t_ff_4 (.clk(Pulse), .T(Toggle), .Qn(out_7), .reset(Clear));  // open: Q, preset, en
endmodule

module Exemplo0072 (
  input  Pulse,
  input  Toggle,
  input  Clear,
  output out_4,
  output out_5,
  output out_6,
  output out_7
);

  wire t_ff_2_qn, t_ff_3_qn, t_ff_4_qn;

  T_Flip_Flop t_ff_1 (.clk(t_ff_2_qn), .T(Toggle), .Q(out_4), .reset(Clear));  // open: Qn, preset, en
  T_Flip_Flop t_ff_2 (.clk(t_ff_3_qn), .T(Toggle), .Q(out_5), .Qn(t_ff_2_qn), .reset(Clear));  // open: preset, en
  T_Flip_Flop t_ff_3 (.clk(t_ff_4_qn), .T(Toggle), .Q(out_6), .Qn(t_ff_3_qn), .reset(Clear));  // open: preset, en
  T_Flip_Flop t_ff_4 (.clk(Pulse), .T(Toggle), .Q(out_7), .Qn(t_ff_4_qn), .reset(Clear));  // open: preset, en
endmodule

module Exemplo0073 (
  input  Toggle,
  input  Pulse,
  input  Clear,
  output out_4,
  output out_5,
  output out_6,
  output out_7
);

  wire and_1_out, not_1_out, not_2_out, or_1_out, t_ff_1_q, t_ff_2_q, t_ff_3_q, t_ff_4_q;

  or or_1 (or_1_out, Clear, and_1_out);
  and and_1 (and_1_out, t_ff_1_q, not_1_out, t_ff_3_q, not_2_out);
  T_Flip_Flop t_ff_1 (.clk(out_5), .T(Toggle), .Q(t_ff_1_q), .Qn(out_4), .reset(or_1_out));  // open: preset, en
  not not_1 (not_1_out, t_ff_2_q);
  not not_2 (not_2_out, t_ff_4_q);
  T_Flip_Flop t_ff_2 (.clk(out_6), .T(Toggle), .Q(t_ff_2_q), .Qn(out_5), .reset(or_1_out));  // open: preset, en
  T_Flip_Flop t_ff_3 (.clk(out_7), .T(Toggle), .Q(t_ff_3_q), .Qn(out_6), .reset(or_1_out));  // open: preset, en
  T_Flip_Flop t_ff_4 (.clk(Pulse), .T(Toggle), .Q(t_ff_4_q), .Qn(out_7), .reset(or_1_out));  // open: preset, en
endmodule

module Exemplo0074 (
  input  Pulse,
  input  Toggle,
  input  Clear,
  output out_4,
  output out_5,
  output out_6,
  output out_7
);

  wire and_1_out, not_1_out, not_2_out, not_3_out, or_1_out, t_ff_2_qn, t_ff_3_qn, t_ff_4_qn;

  not not_1 (not_1_out, Toggle);
  and and_1 (and_1_out, out_4, not_2_out, out_6, not_3_out);
  T_Flip_Flop t_ff_1 (.clk(t_ff_2_qn), .T(Toggle), .Q(out_4), .reset(or_1_out));  // open: Qn, preset, en
  or or_1 (or_1_out, not_1_out, Clear, and_1_out);
  not not_2 (not_2_out, out_5);
  not not_3 (not_3_out, out_7);
  T_Flip_Flop t_ff_2 (.clk(t_ff_3_qn), .T(Toggle), .Q(out_5), .Qn(t_ff_2_qn), .reset(or_1_out));  // open: preset, en
  T_Flip_Flop t_ff_3 (.clk(t_ff_4_qn), .T(Toggle), .Q(out_6), .Qn(t_ff_3_qn), .reset(or_1_out));  // open: preset, en
  T_Flip_Flop t_ff_4 (.clk(Pulse), .T(Toggle), .Q(out_7), .Qn(t_ff_4_qn), .reset(or_1_out));  // open: preset, en
endmodule

module Exemplo0075 (
  input  Pulse,
  input  Clear,
  output out_3,
  output out_4,
  output out_5
);

  wire and_1_out, j_k_ff_2_qn, j_k_ff_3_qn, not_1_out, or_1_out;

  and and_1 (and_1_out, out_3, out_4, not_1_out);
  J_K_Flip_Flop j_k_ff_1 (
    .J(j_k_ff_2_qn), .clk(j_k_ff_2_qn), .K(j_k_ff_2_qn), .Q(out_3), .reset(or_1_out));  // open: Qn, preset, en
  or or_1 (or_1_out, Clear, and_1_out);
  not not_1 (not_1_out, out_5);
  J_K_Flip_Flop j_k_ff_2 (
    .J(j_k_ff_3_qn), .clk(j_k_ff_3_qn), .K(j_k_ff_3_qn), .Q(out_4), .Qn(j_k_ff_2_qn), .reset(or_1_out));  // open: preset, en
  J_K_Flip_Flop j_k_ff_3 (
    .J(Pulse), .clk(Pulse), .K(Pulse), .Q(out_5), .Qn(j_k_ff_3_qn), .reset(or_1_out));  // open: preset, en
endmodule

module Exemplo0076 (
  input  In,
  input  Clear,
  output out_3,
  output out_4,
  output out_5
);

  wire Clock_out, not_1_out, not_2_out, not_3_out, or_1_out;

  Clock Clock (.out(Clock_out));
  or or_1 (or_1_out, out_5, In);
  J_K_Flip_Flop j_k_ff_1 (
    .J(or_1_out), .clk(Clock_out), .K(not_1_out), .Q(out_3), .reset(Clear));  // open: Qn, preset, en
  not not_1 (not_1_out, or_1_out);
  J_K_Flip_Flop j_k_ff_2 (.J(out_3), .clk(Clock_out), .K(not_2_out), .Q(out_4), .reset(Clear));  // open: Qn, preset, en
  not not_2 (not_2_out, out_3);
  J_K_Flip_Flop j_k_ff_3 (.J(out_4), .clk(Clock_out), .K(not_3_out), .Q(out_5), .reset(Clear));  // open: Qn, preset, en
  not not_3 (not_3_out, out_4);
endmodule

module Exemplo0077 (
  input  In,
  input  Clear,
  output out_3,
  output out_4,
  output out_5
);

  wire Clock_out, j_k_ff_3_qn, not_1_out, not_2_out, not_3_out, or_1_out;

  Clock Clock (.out(Clock_out));
  or or_1 (or_1_out, In, j_k_ff_3_qn);
  J_K_Flip_Flop j_k_ff_1 (
    .J(or_1_out), .clk(Clock_out), .K(not_1_out), .Q(out_3), .reset(Clear));  // open: Qn, preset, en
  not not_1 (not_1_out, or_1_out);
  J_K_Flip_Flop j_k_ff_2 (.J(out_3), .clk(Clock_out), .K(not_2_out), .Q(out_4), .reset(Clear));  // open: Qn, preset, en
  not not_2 (not_2_out, out_3);
  J_K_Flip_Flop j_k_ff_3 (
    .J(out_4), .clk(Clock_out), .K(not_3_out), .Q(out_5), .Qn(j_k_ff_3_qn), .reset(Clear));  // open: preset, en
  not not_3 (not_3_out, out_4);
endmodule

module Alternativa_Exemplo0073 (
  input  Pulse,
  input  Toggle,
  input  Clear,
  output out_4,
  output out_5,
  output out_6,
  output out_7
);

  wire d_ff_1_q, nor_1_out, nor_2_out, not_1_out, or_1_out, t_ff_1_q, t_ff_4_q;

  not not_1 (not_1_out, Toggle);
  T_Flip_Flop t_ff_1 (.clk(out_5), .T(Toggle), .Q(t_ff_1_q), .Qn(out_4), .reset(or_1_out));  // open: preset, en
  or or_1 (or_1_out, not_1_out, Clear, d_ff_1_q);
  T_Flip_Flop t_ff_2 (.clk(out_6), .T(Toggle), .Q(out_5), .reset(or_1_out));  // open: Qn, preset, en
  nor nor_1 (nor_1_out, t_ff_4_q, out_6, out_5, t_ff_1_q);
  nor nor_2 (nor_2_out, out_4, out_5, out_7, out_6);
  T_Flip_Flop t_ff_3 (.clk(out_7), .T(Toggle), .Q(out_6), .reset(or_1_out));  // open: Qn, preset, en
  D_Flip_Flop d_ff_1 (.clk(Pulse), .D(nor_2_out), .Q(d_ff_1_q), .reset(nor_1_out));  // open: Qn, preset, en
  T_Flip_Flop t_ff_4 (.clk(Pulse), .T(Toggle), .Q(t_ff_4_q), .Qn(out_7), .reset(or_1_out));  // open: preset, en
endmodule
