// Logisim project Exercicio03.circ as structural Verilog: 1 circuit, main circuit main
module main (
  input  in_1,
  output out_2,
  output out_3,
  output out_4,
  output out_5,
  output out_6
);

  wire and_1_out, clock_1_out, not_1_out, not_2_out, not_3_out, or_1_out, t_ff_1_qn, t_ff_2_qn, t_ff_3_qn,
       t_ff_4_qn, t_ff_5_qn;

  Clock clock_1 (.out(clock_1_out));
  not not_1 (not_1_out, in_1);
  and and_1 (and_1_out, not_2_out, t_ff_2_qn, t_ff_3_qn, not_3_out, t_ff_5_qn);
  T_Flip_Flop t_ff_1 (.clk(clock_1_out), .T(in_1), .Q(out_2), .Qn(t_ff_1_qn), .preset(or_1_out));  // open: reset, en
  or or_1 (or_1_out, not_1_out, and_1_out);
  not not_2 (not_2_out, t_ff_1_qn);
  not not_3 (not_3_out, t_ff_4_qn);
  T_Flip_Flop t_ff_2 (.clk(out_2), .T(in_1), .Q(out_5), .Qn(t_ff_2_qn), .preset(or_1_out));  // open: reset, en
  T_Flip_Flop t_ff_3 (.clk(out_5), .Q(out_4), .Qn(t_ff_3_qn), .preset(or_1_out));  // open: T, reset, en
  T_Flip_Flop t_ff_4 (.clk(out_4), .Q(out_3), .Qn(t_ff_4_qn), .preset(or_1_out));  // open: T, reset, en
  T_Flip_Flop t_ff_5 (.clk(out_3), .T(in_1), .Q(out_2), .Qn(t_ff_5_qn), .preset(or_1_out));  // open: reset, en

  assign out_6 = out_2;

  // Notes on the sheet:
  //   Contador Decádico Decrescente
endmodule
