// Logisim project Exercicio05.circ as structural Verilog: 1 circuit, main circuit main
module main (
  input  in_1,
  output out_2,
  output out_3,
  output out_4
);

  wire and_1_out, clock_1_out, j_k_ff_2_qn, j_k_ff_3_qn, not_1_out, or_1_out;

  Clock clock_1 (.out(clock_1_out));
  or or_1 (or_1_out, in_1, and_1_out);
  J_K_Flip_Flop j_k_ff_1 (.clk(j_k_ff_2_qn), .K(j_k_ff_2_qn), .Q(out_2), .reset(or_1_out));  // open: J, Qn, preset, en
  and and_1 (and_1_out, out_2, not_1_out, out_4);
  J_K_Flip_Flop j_k_ff_2 (
    .clk(j_k_ff_3_qn), .K(j_k_ff_3_qn), .Q(out_3), .Qn(j_k_ff_2_qn), .reset(or_1_out));  // open: J, preset, en
  not not_1 (not_1_out, out_3);
  J_K_Flip_Flop j_k_ff_3 (
    .clk(clock_1_out), .K(clock_1_out), .Q(out_4), .Qn(j_k_ff_3_qn), .reset(or_1_out));  // open: J, preset, en

  // Notes on the sheet:
  //   Contador Modulo 6
endmodule
