// Logisim project Exercicio01.circ as structural Verilog: 1 circuit, main circuit main
module main (
  input  PULSO,
  input  PRESET,
  output out_3,
  output out_4,
  output out_5,
  output out_6
);

  wire CLEAR_out;

  Button CLEAR (.out(CLEAR_out));
  T_Flip_Flop t_ff_1 (.clk(out_4), .T(1'b1), .Qn(out_3), .preset(PRESET), .reset(CLEAR_out));  // open: Q, en
  T_Flip_Flop t_ff_2 (.clk(out_5), .T(1'b1), .Qn(out_4), .preset(PRESET), .reset(CLEAR_out));  // open: Q, en
  T_Flip_Flop t_ff_3 (.clk(out_6), .T(1'b1), .Qn(out_5), .preset(PRESET), .reset(CLEAR_out));  // open: Q, en
  T_Flip_Flop t_ff_4 (.clk(PULSO), .T(1'b1), .Qn(out_6), .preset(PRESET), .reset(CLEAR_out));  // open: Q, en
endmodule
