// Logisim project Exercicio02.circ as structural Verilog: 1 circuit, main circuit main
module main (
  input  PULSO,
  input  PRESET,
  output out_3,
  output out_4,
  output out_5,
  output out_6
);

  wire CLEAR_out, t_ff_2_qn, t_ff_3_qn, t_ff_4_qn;

  Button CLEAR (.out(CLEAR_out));
  T_Flip_Flop t_ff_1 (.clk(t_ff_2_qn), .T(1'b1), .Q(out_3), .preset(PRESET), .reset(CLEAR_out));  // open: Qn, en
  T_Flip_Flop t_ff_2 (
    .clk(t_ff_3_qn), .T(1'b1), .Q(out_4), .Qn(t_ff_2_qn), .preset(PRESET), .reset(CLEAR_out));  // open: en
  T_Flip_Flop t_ff_3 (
    .clk(t_ff_4_qn), .T(1'b1), .Q(out_5), .Qn(t_ff_3_qn), .preset(PRESET), .reset(CLEAR_out));  // open: en
  T_Flip_Flop t_ff_4 (
    .clk(PULSO), .T(1'b1), .Q(out_6), .Qn(t_ff_4_qn), .preset(PRESET), .reset(CLEAR_out));  // open: en
endmodule
