// Logisim project Exercicio03.circ as structural Verilog: 1 circuit, main circuit main
module main (
  input  PULSO,
  input  PRESET,
  input  Clear,
  output out_4,
  output out_5,
  output out_6,
  output out_7
);

  wire and_1_out, or_1_out, t_ff_1_q, t_ff_3_q;

  or or_1 (or_1_out, Clear, and_1_out);
  T_Flip_Flop t_ff_1 (.clk(out_5), .T(1'b1), .Q(t_ff_1_q), .Qn(out_4), .preset(PRESET), .reset(or_1_out));  // open: en
  and and_1 (and_1_out, t_ff_1_q, out_5, t_ff_3_q, out_7);
  T_Flip_Flop t_ff_2 (.clk(out_6), .T(1'b1), .Qn(out_5), .preset(PRESET), .reset(or_1_out));  // open: Q, en
  T_Flip_Flop t_ff_3 (.clk(out_7), .T(1'b1), .Q(t_ff_3_q), .Qn(out_6), .preset(PRESET), .reset(or_1_out));  // open: en
  T_Flip_Flop t_ff_4 (.clk(PULSO), .T(1'b1), .Qn(out_7), .preset(PRESET), .reset(or_1_out));  // open: Q, en
endmodule
