// Logisim project Exercicio05.circ as structural Verilog: 1 circuit, main circuit main
module main (
  input  in_1,
  input  in_2,
  input  in_3,
  output out_4,
  output out_5,
  output out_6
);

  wire and_1_out, j_k_ff_2_qn, j_k_ff_3_qn, or_1_out;

  or or_1 (or_1_out, in_3, and_1_out);
  and and_1 (and_1_out, out_4, out_5, j_k_ff_3_qn);
  J_K_Flip_Flop j_k_ff_1 (
    .J(j_k_ff_2_qn), .clk(j_k_ff_2_qn), .K(j_k_ff_2_qn), .Q(out_4), .preset(in_2), .reset(or_1_out));  // open: Qn, en
  J_K_Flip_Flop j_k_ff_2 (
    .J(j_k_ff_3_qn), .clk(j_k_ff_3_qn), .K(j_k_ff_3_qn), .Q(out_5), .Qn(j_k_ff_2_qn), .preset(in_2),
    .reset(or_1_out));  // open: en
  J_K_Flip_Flop j_k_ff_3 (
    .J(in_1), .clk(in_1), .K(in_1), .Q(out_6), .Qn(j_k_ff_3_qn), .preset(in_2), .reset(or_1_out));  // open: en
endmodule
