// Logisim project Exercicio03.circ as structural Verilog: 3 circuits, main circuit main
module main (
  input  Addr,
  input  R_W,
  input  CLK,
  input  IN,
  input  Clr,
  output Out
);

  wire And01_out, j_k_ff_1_q;

  and And01 (And01_out, Addr, R_W, CLK);
  J_K_Flip_Flop j_k_ff_1 (.J(And01_out), .K(IN), .Q(j_k_ff_1_q), .reset(Clr));  // open: clk, Qn, preset, en
  J_K_Flip_Flop j_k_ff_2 (.J(And01_out), .K(IN), .Q(j_k_ff_1_q));  // open: clk, Qn, preset, en, reset
  J_K_Flip_Flop j_k_ff_3 (.J(And01_out), .K(IN), .Q(j_k_ff_1_q));  // open: clk, Qn, preset, en, reset
  J_K_Flip_Flop j_k_ff_4 (.J(And01_out), .K(IN), .Q(j_k_ff_1_q));  // open: clk, Qn, preset, en, reset
  and And02 (Out, j_k_ff_1_q, Addr);

  // Notes on the sheet:
  //   Jorge Luis dos Santos Leal
  //   RAM - 1X4
endmodule

module RAM1X4 (
  input  Addr,
  input  R_W,
  input  Clk,
  input  IN00,
  input  IN01,
  input  CLR,
  output OUT00,
  output OUT01
);

  main main_1 (.Addr(IN00), .R_W(Clk), .CLK(R_W), .IN(Addr), .Clr(CLR), .Out(OUT00));
  main main_2 (.Addr(IN01), .R_W(Clk), .CLK(R_W), .IN(Addr), .Clr(CLR), .Out(OUT01));

  // Notes on the sheet:
  //   Jorge Luis dos Santos Leal
  //   RAM - 1x8 (2 1X4)
endmodule

module RAM1x8 (
  input  Addr,
  input  R_W,
  input  Clk,
  input  IN00,
  input  IN01,
  input  IN02,
  input  IN03,
  input  CLR,
  output OUT00,
  output OUT01,
  output OUT02,
  output OUT03
);

  main main_1 (.Addr(IN00), .R_W(Clk), .CLK(R_W), .IN(Addr), .Clr(CLR), .Out(OUT00));
  main main_2 (.Addr(IN01), .R_W(Clk), .CLK(R_W), .IN(Addr), .Clr(CLR), .Out(OUT01));
  main main_3 (.Addr(IN02), .R_W(Clk), .CLK(R_W), .IN(Addr), .Clr(CLR), .Out(OUT02));
  main main_4 (.Addr(IN03), .R_W(Clk), .CLK(R_W), .IN(Addr), .Clr(CLR), .Out(OUT03));

  // Notes on the sheet:
  //   Jorge Luis dos Santos Leal
  //   RAM - 4x8 (4 1X8)
endmodule
