// Logisim project Exercicio04.circ as structural Verilog: 1 circuit, main circuit main
module main (
  input  Addr,
  input  R_W,
  input  CLK,
  input  IN,
  input  Clr,
  output Out
);

  wire And01_out, j_k_ff_1_q;

  and And01 (And01_out, Addr, R_W, CLK);
  J_K_Flip_Flop j_k_ff_1 (.J(And01_out), .K(IN), .Q(j_k_ff_1_q), .reset(Clr));  // open: clk, Qn, preset, en
  J_K_Flip_Flop j_k_ff_2 (.J(And01_out), .K(IN), .Q(j_k_ff_1_q));  // open: clk, Qn, preset, en, reset
  J_K_Flip_Flop j_k_ff_3 (.J(And01_out), .K(IN), .Q(j_k_ff_1_q));  // open: clk, Qn, preset, en, reset
  J_K_Flip_Flop j_k_ff_4 (.J(And01_out), .K(IN), .Q(j_k_ff_1_q));  // open: clk, Qn, preset, en, reset
  J_K_Flip_Flop j_k_ff_5 (.J(And01_out), .K(IN), .Q(j_k_ff_1_q));  // open: clk, Qn, preset, en, reset
  J_K_Flip_Flop j_k_ff_6 (.J(And01_out), .K(IN), .Q(j_k_ff_1_q));  // open: clk, Qn, preset, en, reset
  J_K_Flip_Flop j_k_ff_7 (.J(And01_out), .K(IN), .Q(j_k_ff_1_q));  // open: clk, Qn, preset, en, reset
  J_K_Flip_Flop j_k_ff_8 (.J(And01_out), .K(IN), .Q(j_k_ff_1_q));  // open: clk, Qn, preset, en, reset
  and And02 (Out, j_k_ff_1_q, Addr);

  // Notes on the sheet:
  //   Jorge Luis dos Santos Leal
  //   RAM - 1X8
endmodule
