// Logisim project Extra02.circ as structural Verilog: 3 circuits, main circuit main
module main (
  input  Addr,
  input  R_W,
  input  CLK,
  input  IN,
  input  Clr,
  output Out
);

  wire And01_out, j_k_ff_1_q;

  and And01 (And01_out, Addr, R_W, CLK);
  J_K_Flip_Flop j_k_ff_1 (.J(And01_out), .K(IN), .Q(j_k_ff_1_q), .reset(Clr));  // open: clk, Qn, preset, en
  J_K_Flip_Flop j_k_ff_2 (.J(And01_out), .K(IN), .Q(j_k_ff_1_q));  // open: clk, Qn, preset, en, reset
  J_K_Flip_Flop j_k_ff_3 (.J(And01_out), .K(IN), .Q(j_k_ff_1_q));  // open: clk, Qn, preset, en, reset
  J_K_Flip_Flop j_k_ff_4 (.J(And01_out), .K(IN), .Q(j_k_ff_1_q));  // open: clk, Qn, preset, en, reset
  and And02 (Out, j_k_ff_1_q, Addr);

  // Notes on the sheet:
  //   Jorge Luis dos Santos Leal
  //   RAM - 1X4
endmodule

module RAM1X4 (
  input  Addr,
  input  R_W,
  input  Clk,
  input  IN00,
  input  IN01,
  input  IN02,
  input  IN03,
  input  CLR,
  output OUT00,
  output OUT01,
  output OUT02,
  output OUT02_2
);

  main main_1 (.Addr(IN00), .R_W(Clk), .CLK(R_W), .IN(Addr), .Clr(CLR), .Out(OUT00));
  main main_2 (.Addr(IN01), .R_W(Clk), .CLK(R_W), .IN(Addr), .Clr(CLR), .Out(OUT01));
  main main_3 (.Addr(IN02), .R_W(Clk), .CLK(R_W), .IN(Addr), .Clr(CLR), .Out(OUT02));
  main main_4 (.Addr(IN03), .R_W(Clk), .CLK(R_W), .IN(Addr), .Clr(CLR), .Out(OUT02_2));

  // Notes on the sheet:
  //   Jorge Luis dos Santos Leal
  //   RAM - 1x16 (4 1X4)
endmodule

module RAM1x8 (
  input  Addr,
  input  R_W,
  input  Clk,
  input  IN00,
  input  IN01,
  input  IN02,
  input  IN03,
  input  IN04,
  input  IN05,
  input  IN06,
  input  IN07,
  input  CLR,
  output OUT00,
  output OUT01,
  output OUT02,
  output OUT02_2
);

  main main_1 (.Addr(IN00), .R_W(Clk), .CLK(R_W), .IN(Addr), .Clr(CLR), .Out(OUT00));
  main main_2 (.Addr(IN01), .R_W(Clk), .CLK(R_W), .IN(Addr), .Clr(CLR), .Out(OUT01));
  main main_3 (.Addr(IN02), .R_W(Clk), .CLK(R_W), .IN(Addr), .Clr(CLR), .Out(OUT02));
  main main_4 (.Addr(IN03), .R_W(Clk), .CLK(R_W), .IN(Addr), .Clr(CLR), .Out(OUT02_2));
  main main_5 (.Addr(IN04), .R_W(Clk), .CLK(R_W), .IN(Addr), .Clr(CLR));  // open: Out
  main main_6 (.Addr(IN05), .R_W(Clk), .CLK(R_W), .IN(Addr), .Clr(CLR));  // open: Out
  main main_7 (.Addr(IN06), .R_W(Clk), .CLK(R_W), .IN(Addr), .Clr(CLR));  // open: Out
  main main_8 (.Addr(IN07), .R_W(Clk), .CLK(R_W), .IN(Addr), .Clr(CLR));  // open: Out

  // Notes on the sheet:
  //   Jorge Luis dos Santos Leal
  //   RAM - 4x16 (8 1X8)
endmodule
