// Logisim project exercicio01.circ as structural Verilog: 3 circuits, main circuit 1x1
module _1x1 (
  input  in_1,
  input  in_2,
  input  CLK,
  input  in_4,
  input  in_5,
  output out_6
);

  wire and_1_out, j_k_ff_1_q, not_1_out;

  not not_1 (not_1_out, in_4);
  and and_1 (and_1_out, in_1, in_2, CLK);
  J_K_Flip_Flop j_k_ff_1 (
    .J(in_4), .clk(and_1_out), .K(not_1_out), .Q(j_k_ff_1_q), .reset(in_5));  // open: Qn, preset, en
  and and_2 (out_6, in_1, j_k_ff_1_q);
endmodule

module _1x4 (
  input  in_1,
  input  in_2,
  input  CLK,
  input  [3:0] in_4,
  input  in_5,
  output [3:0] out_6
);

  _1x2 u_1x2_1 (
    .in_1(in_1), .in_2(in_2), .CLK(CLK), .in_4(in_4[0]), .in_5(in_4[1]), .CLR(in_5), .out_7(out_6[0]),
    .out_8(out_6[1]));
  _1x2 u_1x2_2 (
    .in_1(in_1), .in_2(in_2), .CLK(CLK), .in_4(in_4[2]), .in_5(in_4[3]), .CLR(in_5), .out_7(out_6[2]),
    .out_8(out_6[3]));
endmodule

module _1x2 (
  input  in_1,
  input  in_2,
  input  CLK,
  input  in_4,
  input  in_5,
  input  CLR,
  output out_7,
  output out_8
);

  _1x1 u_1x1_1 (.in_1(in_1), .in_2(in_2), .CLK(CLK), .in_4(in_4), .in_5(CLR), .out_6(out_8));
  _1x1 u_1x1_2 (.in_1(in_1), .in_2(in_2), .CLK(CLK), .in_4(in_5), .in_5(CLR), .out_6(out_7));
endmodule
