// Logisim project exercicio03.circ as structural Verilog: 6 circuits, main circuit 1x1
module _1x1 (
  input  ADDR,
  input  R_W,
  input  CLK,
  input  IN,
  input  in_5,
  output out_6
);

  wire and_1_out, j_k_ff_1_q, not_1_out;

  and and_1 (and_1_out, ADDR, R_W, CLK);
  not not_1 (not_1_out, IN);
  J_K_Flip_Flop j_k_ff_1 (
    .J(IN), .clk(and_1_out), .K(not_1_out), .Q(j_k_ff_1_q), .reset(in_5));  // open: Qn, preset, en
  and and_2 (out_6, ADDR, j_k_ff_1_q);
endmodule

module _1x4 (
  input  ADDR,
  input  R_W,
  input  CLK,
  input  [3:0] in_4,
  input  in_5,
  output [3:0] out_6
);

  _1x2 u_1x2_1 (
    .ADDR(ADDR), .R_W(R_W), .CLK(CLK), .IN_1(in_4[0]), .IN_2(in_4[1]), .CLR(in_5), .out_7(out_6[0]),
    .out_8(out_6[1]));
  _1x2 u_1x2_2 (
    .ADDR(ADDR), .R_W(R_W), .CLK(CLK), .IN_1(in_4[2]), .IN_2(in_4[3]), .CLR(in_5), .out_7(out_6[2]),
    .out_8(out_6[3]));
endmodule

module _1x2 (
  input  ADDR,
  input  R_W,
  input  CLK,
  input  IN_1,
  input  IN_2,
  input  CLR,
  output out_7,
  output out_8
);

  _1x1 u_1x1_1 (.ADDR(ADDR), .R_W(R_W), .CLK(CLK), .IN(IN_1), .in_5(CLR), .out_6(out_8));
  _1x1 u_1x1_2 (.ADDR(ADDR), .R_W(R_W), .CLK(CLK), .IN(IN_2), .in_5(CLR), .out_6(out_7));
endmodule

module _1x8 (
  input  ADD,
  input  R_W,
  input  CLK,
  input  [7:0] in_4,
  input  in_5,
  output [7:0] out_6
);

  _1x4 u_1x4_1 (.ADDR(ADD), .R_W(R_W), .CLK(CLK), .in_4(in_4[3:0]), .in_5(in_5), .out_6(out_6[7:4]));
  _1x4 u_1x4_2 (.ADDR(ADD), .R_W(R_W), .CLK(CLK), .in_4(in_4[7:4]), .in_5(in_5), .out_6(out_6[3:0]));
endmodule

module _2x2 (
  input  in_1,
  input  in_2,
  input  in_3,
  input  [1:0] in_4,
  input  in_5,
  output [1:0] out_6
);

  wire demultiplexer_1_out0, demultiplexer_1_out1;
  wire [1:0] n1x2_1_out_7, n1x2_2_out_7;

  Demultiplexer demultiplexer_1 (
    .out0(demultiplexer_1_out0), .out1(demultiplexer_1_out1), .in(1'b1), .sel(in_1));  // open: en
  _1x2 u_1x2_1 (
    .ADDR(demultiplexer_1_out0), .R_W(in_2), .CLK(in_3), .IN_1(in_4[0]), .IN_2(in_4[1]), .CLR(in_5),
    .out_7(n1x2_1_out_7[0]), .out_8(n1x2_1_out_7[1]));
  _1x2 u_1x2_2 (
    .ADDR(demultiplexer_1_out1), .R_W(in_3), .CLK(in_2), .IN_1(in_4[0]), .IN_2(in_4[1]), .CLR(in_5),
    .out_7(n1x2_2_out_7[0]), .out_8(n1x2_2_out_7[1]));
  Multiplexer #(.width(2)) multiplexer_1 (.in0(n1x2_1_out_7), .in1(n1x2_2_out_7), .out(out_6), .sel(in_1));  // open: en
endmodule

module _4x4__main (
  input  in_1,
  input  in_2,
  input  in_3,
  input  [3:0] in_4,
  input  in_5,
  output [3:0] out_6
);

  wire demultiplexer_1_out0, demultiplexer_1_out1;
  wire [1:0] n2x2_1_out_6, n2x2_2_out_6;

  Demultiplexer demultiplexer_1 (
    .out0(demultiplexer_1_out0), .out1(demultiplexer_1_out1), .in(1'b1), .sel(in_1));  // open: en
  _2x2 u_2x2_1 (
    .in_1(demultiplexer_1_out0), .in_2(in_2), .in_3(in_3), .in_4(in_4[1:0]), .in_5(in_5), .out_6(n2x2_1_out_6));
  _2x2 u_2x2_2 (
    .in_1(demultiplexer_1_out1), .in_2(in_2), .in_3(in_3), .in_4(in_4[3:2]), .in_5(in_5), .out_6(n2x2_2_out_6));
  Multiplexer #(.width(4)) multiplexer_1 (
    .in0({n2x2_2_out_6, n2x2_1_out_6}), .in1({n2x2_2_out_6, n2x2_1_out_6}), .out(out_6), .sel(in_1));  // open: en
endmodule
