// Logisim project circuitos.circ as structural Verilog: 8 circuits, main circuit 1x2
module _1x4_JK (
  input  CLK,
  input  R_W,
  input  ADDR,
  input  CLR,
  input  [3:0] IN,
  output [3:0] OUT
);

  wire and_1_out, j_k_ff_1_q, j_k_ff_2_q, j_k_ff_3_q, j_k_ff_4_q;

  and and_1 (and_1_out, CLK, R_W, ADDR);
  J_K_Flip_Flop j_k_ff_1 (.J(IN[0]), .clk(and_1_out), .K(IN[0]), .Q(j_k_ff_1_q), .reset(CLR));  // open: Qn, preset, en
  J_K_Flip_Flop j_k_ff_2 (.J(IN[1]), .clk(and_1_out), .K(IN[1]), .Q(j_k_ff_2_q), .reset(CLR));  // open: Qn, preset, en
  J_K_Flip_Flop j_k_ff_3 (.J(IN[2]), .clk(and_1_out), .K(IN[2]), .Q(j_k_ff_3_q), .reset(CLR));  // open: Qn, preset, en
  J_K_Flip_Flop j_k_ff_4 (.J(IN[3]), .clk(and_1_out), .K(IN[3]), .Q(j_k_ff_4_q), .reset(CLR));  // open: Qn, preset, en
  and and_2 (OUT[0], j_k_ff_1_q, ADDR);
  and and_3 (OUT[1], j_k_ff_2_q, ADDR);
  and and_4 (OUT[2], j_k_ff_3_q, ADDR);
  and and_5 (OUT[3], j_k_ff_4_q, ADDR);

  // Notes on the sheet:
  //   RAM 1x4 usando FF JK
endmodule

module _1x4 (
  input  ADDR,
  input  R_W,
  input  CLK,
  input  IN_0,
  input  IN_1,
  input  IN_2,
  input  IN_3,
  input  CLR,
  output OUT_0,
  output OUT_1,
  output OUT_2,
  output OUT_3
);

  _1x2 u_1x2_1 (.ADDR(ADDR), .R_W(R_W), .CLK(CLK), .IN_0(IN_0), .IN_1(IN_1), .CLR(CLR), .OUT_0(OUT_0), .OUT_1(OUT_1));
  _1x2 u_1x2_2 (.ADDR(ADDR), .R_W(R_W), .CLK(CLK), .IN_0(IN_2), .IN_1(IN_3), .CLR(CLR), .OUT_0(OUT_2), .OUT_1(OUT_3));
endmodule

module _1x2 (
  input  ADDR,
  input  R_W,
  input  CLK,
  input  IN_0,
  input  IN_1,
  input  CLR,
  output OUT_0,
  output OUT_1
);

  _1x1 u_1x1_1 (.ADDR(ADDR), .R_W(R_W), .CLK(CLK), .IN(IN_0), .CLR(CLR), .OUT(OUT_0));
  _1x1 u_1x1_2 (.ADDR(ADDR), .R_W(R_W), .CLK(CLK), .IN(IN_1), .CLR(CLR), .OUT(OUT_1));
endmodule

module _1x1 (
  input  ADDR,
  input  R_W,
  input  CLK,
  input  IN,
  input  CLR,
  output OUT
);

  wire and_1_out, j_k_ff_1_q;

  and and_1 (and_1_out, ADDR, R_W, CLK);
  J_K_Flip_Flop j_k_ff_1 (.J(IN), .clk(and_1_out), .K(IN), .Q(j_k_ff_1_q), .reset(CLR));  // open: Qn, preset, en
  and and_2 (OUT, ADDR, j_k_ff_1_q);
endmodule

module _1x8 (
  input  CLR,
  input  CLK,
  input  R_W,
  input  ADDR,
  input  IN_3,
  input  IN_4,
  input  IN_2,
  input  IN_5,
  input  IN_6,
  input  IN_1,
  input  IN_7,
  input  IN_0,
  output OUT0,
  output OUT1,
  output OUT2,
  output OUT3,
  output OUT4,
  output OUT5,
  output OUT6,
  output OUT7
);

  _1x4 u_1x4_1 (
    .ADDR(ADDR), .R_W(R_W), .CLK(CLK), .IN_0(IN_3), .IN_1(IN_2), .IN_2(IN_1), .IN_3(IN_0), .CLR(CLR),
    .OUT_0(OUT3), .OUT_1(OUT2), .OUT_2(OUT1), .OUT_3(OUT0));
  _1x4 u_1x4_2 (
    .ADDR(ADDR), .R_W(R_W), .CLK(CLK), .IN_0(IN_7), .IN_1(IN_6), .IN_2(IN_5), .IN_3(IN_4), .CLR(CLR),
    .OUT_0(OUT7), .OUT_1(OUT6), .OUT_2(OUT5), .OUT_3(OUT4));
endmodule

module _4x8 (
  input  [3:0] ADDR,
  input  CLR,
  input  R_W,
  input  CLK,
  input  [7:0] IN,
  output [7:0] OUT
);

  wire demultiplexer_1_out0, demultiplexer_1_out1, demultiplexer_1_out2, demultiplexer_1_out3;
  wire [7:0] n1x8_jk_1_out, n1x8_jk_2_out, n1x8_jk_3_out, n1x8_jk_4_out;

  Demultiplexer #(.select(4), .enable("false")) demultiplexer_1 (
    .out0(demultiplexer_1_out0), .out1(demultiplexer_1_out1), .out2(demultiplexer_1_out2),
    .out3(demultiplexer_1_out3), .in(1'b1), .sel(ADDR));  // open: out4, out5, out6, out7, out8, out9, out10, out11, out12, out13, out14, out15
  _1x8_JK u_1x8_jk_1 (.IN(IN), .CLK(CLK), .R_W(R_W), .ADDR(demultiplexer_1_out0), .CLR(CLR), .OUT(n1x8_jk_1_out));
  _1x8_JK u_1x8_jk_2 (.IN(IN), .CLK(CLK), .R_W(R_W), .ADDR(demultiplexer_1_out1), .CLR(CLR), .OUT(n1x8_jk_2_out));
  _1x8_JK u_1x8_jk_3 (.IN(IN), .CLK(CLK), .R_W(R_W), .ADDR(demultiplexer_1_out2), .CLR(CLR), .OUT(n1x8_jk_3_out));
  _1x8_JK u_1x8_jk_4 (.IN(IN), .CLK(CLK), .R_W(R_W), .ADDR(demultiplexer_1_out3), .CLR(CLR), .OUT(n1x8_jk_4_out));
  Multiplexer #(.select(4), .width(8), .enable("false")) multiplexer_1 (
    .in0(n1x8_jk_1_out), .in1(n1x8_jk_2_out), .in2(n1x8_jk_3_out), .in3(n1x8_jk_4_out), .out(OUT), .sel(ADDR));  // open: in4, in5, in6, in7, in8, in9, in10, in11, in12, in13, in14, in15
endmodule

// 1x8
module _1x8_JK (
  input  CLK,
  input  R_W,
  input  ADDR,
  input  CLR,
  input  [7:0] IN,
  output [7:0] OUT
);

  wire and_1_out, j_k_ff_1_q, j_k_ff_2_q, j_k_ff_3_q, j_k_ff_4_q, j_k_ff_5_q, j_k_ff_6_q, j_k_ff_7_q,
       j_k_ff_8_q;

  and and_1 (and_1_out, CLK, R_W, ADDR);
  J_K_Flip_Flop j_k_ff_1 (.J(IN[0]), .clk(and_1_out), .K(IN[0]), .Q(j_k_ff_1_q), .reset(CLR));  // open: Qn, preset, en
  J_K_Flip_Flop j_k_ff_2 (.J(IN[1]), .clk(and_1_out), .K(IN[1]), .Q(j_k_ff_2_q), .reset(CLR));  // open: Qn, preset, en
  J_K_Flip_Flop j_k_ff_3 (.J(IN[2]), .clk(and_1_out), .K(IN[2]), .Q(j_k_ff_3_q), .reset(CLR));  // open: Qn, preset, en
  J_K_Flip_Flop j_k_ff_4 (.J(IN[3]), .clk(and_1_out), .K(IN[3]), .Q(j_k_ff_4_q), .reset(CLR));  // open: Qn, preset, en
  J_K_Flip_Flop j_k_ff_5 (.J(IN[4]), .clk(and_1_out), .K(IN[4]), .Q(j_k_ff_5_q), .reset(CLR));  // open: Qn, preset, en
  J_K_Flip_Flop j_k_ff_6 (.J(IN[5]), .clk(and_1_out), .K(IN[5]), .Q(j_k_ff_6_q), .reset(CLR));  // open: Qn, preset, en
  J_K_Flip_Flop j_k_ff_7 (.J(IN[6]), .clk(and_1_out), .K(IN[6]), .Q(j_k_ff_7_q), .reset(CLR));  // open: Qn, preset, en
  J_K_Flip_Flop j_k_ff_8 (.J(IN[7]), .clk(and_1_out), .K(IN[7]), .Q(j_k_ff_8_q), .reset(CLR));  // open: Qn, preset, en
  and and_2 (OUT[0], j_k_ff_1_q, ADDR);
  and and_3 (OUT[1], j_k_ff_2_q, ADDR);
  and and_4 (OUT[2], j_k_ff_3_q, ADDR);
  and and_5 (OUT[3], j_k_ff_4_q, ADDR);
  and and_6 (OUT[4], j_k_ff_5_q, ADDR);
  and and_7 (OUT[5], j_k_ff_6_q, ADDR);
  and and_8 (OUT[6], j_k_ff_7_q, ADDR);
  and and_9 (OUT[7], j_k_ff_8_q, ADDR);

  // Notes on the sheet:
  //   RAM 1x8 usando FF JK
endmodule

module _1x16 (
  input  CLR,
  input  CLK,
  input  R_W,
  input  ADDR,
  input  IN_3,
  input  IN_4,
  input  IN_8,
  input  IN12,
  input  IN_2,
  input  IN_5,
  input  IN_9,
  input  IN13,
  input  IN_6,
  input  IN14,
  input  IN_1,
  input  IN10,
  input  IN_7,
  input  IN15,
  input  IN_0,
  input  IN11,
  output OUT0,
  output OUT1,
  output OUT2,
  output OUT3,
  output OUT4,
  output OUT5,
  output OUT6,
  output OUT7,
  output OUT8,
  output OUT9,
  output OUT10,
  output OUT11,
  output OUT12,
  output OUT13,
  output OUT14,
  output OUT15
);

  _1x4 u_1x4_1 (
    .ADDR(ADDR), .R_W(R_W), .CLK(CLK), .IN_0(IN_3), .IN_1(IN_2), .IN_2(IN_1), .IN_3(IN_0), .CLR(CLR),
    .OUT_0(OUT3), .OUT_1(OUT2), .OUT_2(OUT1), .OUT_3(OUT0));
  _1x4 u_1x4_2 (
    .ADDR(ADDR), .R_W(R_W), .CLK(CLK), .IN_0(IN_7), .IN_1(IN_6), .IN_2(IN_5), .IN_3(IN_4), .CLR(CLR),
    .OUT_0(OUT7), .OUT_1(OUT6), .OUT_2(OUT5), .OUT_3(OUT4));
  _1x4 u_1x4_3 (
    .ADDR(ADDR), .R_W(R_W), .CLK(CLK), .IN_0(IN_8), .IN_1(IN_9), .IN_2(IN10), .IN_3(IN11), .CLR(CLR),
    .OUT_0(OUT11), .OUT_1(OUT10), .OUT_2(OUT9), .OUT_3(OUT8));
  _1x4 u_1x4_4 (
    .ADDR(ADDR), .R_W(R_W), .CLK(CLK), .IN_0(IN15), .IN_1(IN14), .IN_2(IN13), .IN_3(IN12), .CLR(CLR),
    .OUT_0(OUT15), .OUT_1(OUT14), .OUT_2(OUT13), .OUT_3(OUT12));

  // Notes on the sheet:
  //   RAM 1x16 usando quatro memórias RAM 1x4
endmodule
