// Logisim project Projetos.circ as structural Verilog
// 1X4
module Exercicio01 (
  input  CLOCK,
  input  [3:0] _input,
  input  R_W,
  input  ADDRES,
  input  CLR,
  output [3:0] _output
);

  wire and_1_out, and_2_out, not_1_out, not_2_out, not_3_out, not_4_out;
  wire [3:0] _0_q;

  not not_1 (not_1_out, _input[3]);
  and and_1 (and_1_out, R_W, ADDRES, CLOCK);
  J_K_Flip_Flop _3 (.J(_input[3]), .clk(and_1_out), .K(not_1_out), .Q(_0_q[3]), .reset(CLR));  // open: Qn, preset, en
  not not_2 (not_2_out, _input[2]);
  J_K_Flip_Flop _2 (.J(_input[2]), .clk(and_1_out), .K(not_2_out), .Q(_0_q[2]), .reset(CLR));  // open: Qn, preset, en
  not not_3 (not_3_out, _input[1]);
  J_K_Flip_Flop _1 (.J(_input[1]), .clk(and_1_out), .K(not_3_out), .Q(_0_q[1]), .reset(CLR));  // open: Qn, preset, en
  J_K_Flip_Flop _0 (.J(_input[0]), .clk(and_1_out), .K(not_4_out), .Q(_0_q[0]), .reset(CLR));  // open: Qn, preset, en
  not not_4 (not_4_out, _input[0]);
  and and_2 (and_2_out, ~CLOCK, ~R_W, ADDRES);  // AND_Gate
  assign _output = and_2_out ? _0_q : 4'bz;  // Controlled_Buffer controlled_buffer_1
endmodule

// 1X8
module Exercicio02 (
  input  CLOCK,
  input  [7:0] \input ,
  input  R_W,
  input  ADDRES,
  input  CLR,
  output [7:0] \output 
);

  Exercicio01 _3_0 (
    .CLOCK(CLOCK), .R_W(R_W), .ADDRES(ADDRES), .CLR(CLR), ._input(\input [3:0]), ._output(\output [3:0]));
  Exercicio01 _7_4 (
    .CLOCK(CLOCK), .R_W(R_W), .ADDRES(ADDRES), .CLR(CLR), ._input(\input [7:4]), ._output(\output [7:4]));
endmodule

module Exercicio03 (
  input  [7:0] \input ,
  input  CLOCK,
  input  R_W,
  input  [1:0] ADDRES,
  input  CLEAR,
  output [7:0] \output 
);

  wire demultiplexer_1_out0, demultiplexer_1_out1, demultiplexer_1_out2, demultiplexer_1_out3;
  wire [7:0] _0_output, _1_output, _2_output, _3_output;

  Demultiplexer #(.select(2)) demultiplexer_1 (
    .out0(demultiplexer_1_out0), .out1(demultiplexer_1_out1), .out2(demultiplexer_1_out2),
    .out3(demultiplexer_1_out3), .in(1'b1), .sel(ADDRES));  // open: en
  Exercicio02 _0 (
    .CLOCK(CLOCK), .R_W(R_W), .ADDRES(demultiplexer_1_out0), .CLR(CLEAR), .\input (\input ),
    .\output (_0_output));
  Exercicio02 _1 (
    .CLOCK(CLOCK), .R_W(R_W), .ADDRES(demultiplexer_1_out1), .CLR(CLEAR), .\input (\input ),
    .\output (_1_output));
  Exercicio02 _2 (
    .CLOCK(CLOCK), .R_W(R_W), .ADDRES(demultiplexer_1_out2), .CLR(CLEAR), .\input (\input ),
    .\output (_2_output));
  Exercicio02 _3 (
    .CLOCK(CLOCK), .R_W(R_W), .ADDRES(demultiplexer_1_out3), .CLR(CLEAR), .\input (\input ),
    .\output (_3_output));
  Multiplexer #(.select(2), .width(8)) multiplexer_1 (
    .in0(_0_output), .in1(_1_output), .in2(_2_output), .in3(_3_output), .out(\output ), .sel(ADDRES));  // open: en
endmodule

// 1x8
module Exercicio04 (
  input  CLOCK,
  input  [7:0] _input,
  input  R_W,
  input  ADDRES,
  input  CLR,
  output [7:0] _output
);

  wire and_1_out, and_2_out, not_1_out, not_2_out, not_3_out, not_4_out, not_5_out, not_6_out, not_7_out,
       not_8_out;
  wire [7:0] _0_q;

  and and_1 (and_1_out, R_W, ADDRES, CLOCK);
  J_K_Flip_Flop _3 (.J(_input[3]), .clk(and_1_out), .K(not_1_out), .Q(_0_q[3]), .reset(CLR));  // open: Qn, preset, en
  not not_1 (not_1_out, _input[3]);
  not not_2 (not_2_out, _input[7]);
  not not_3 (not_3_out, _input[2]);
  J_K_Flip_Flop _7 (.J(_input[7]), .clk(and_1_out), .K(not_2_out), .Q(_0_q[7]), .reset(CLR));  // open: Qn, preset, en
  not not_4 (not_4_out, _input[6]);
  J_K_Flip_Flop _2 (.J(_input[2]), .clk(and_1_out), .K(not_3_out), .Q(_0_q[2]), .reset(CLR));  // open: Qn, preset, en
  J_K_Flip_Flop _6 (.J(_input[6]), .clk(and_1_out), .K(not_4_out), .Q(_0_q[6]), .reset(CLR));  // open: Qn, preset, en
  J_K_Flip_Flop _1 (.J(_input[1]), .clk(and_1_out), .K(not_5_out), .Q(_0_q[1]), .reset(CLR));  // open: Qn, preset, en
  not not_5 (not_5_out, _input[1]);
  J_K_Flip_Flop _5 (.J(_input[5]), .clk(and_1_out), .K(not_6_out), .Q(_0_q[5]), .reset(CLR));  // open: Qn, preset, en
  not not_6 (not_6_out, _input[5]);
  not not_7 (not_7_out, _input[0]);
  not not_8 (not_8_out, _input[4]);
  J_K_Flip_Flop _0 (.J(_input[0]), .clk(and_1_out), .K(not_7_out), .Q(_0_q[0]), .reset(CLR));  // open: Qn, preset, en
  J_K_Flip_Flop _4 (.J(_input[4]), .clk(and_1_out), .K(not_8_out), .Q(_0_q[4]), .reset(CLR));  // open: Qn, preset, en
  and and_2 (and_2_out, ~CLOCK, ~R_W, ADDRES);  // AND_Gate
  assign _output = and_2_out ? _0_q : 8'bz;  // Controlled_Buffer controlled_buffer_1
endmodule

module Exercicio05 (
  input  [7:0] \input ,
  input  CLOCK,
  input  R_W,
  input  [2:0] ADDRES,
  input  CLEAR,
  output [7:0] \output 
);

  wire demultiplexer_1_out0, demultiplexer_1_out1, demultiplexer_1_out2, demultiplexer_1_out3,
       demultiplexer_1_out4, demultiplexer_1_out5, demultiplexer_1_out6, demultiplexer_1_out7;
  wire [7:0] _0__output, _1__output, _2__output, _3__output, _4__output, _5__output, _6__output, _7__output;

  Demultiplexer #(.select(3)) demultiplexer_1 (
    .out0(demultiplexer_1_out0), .out1(demultiplexer_1_out1), .out2(demultiplexer_1_out2),
    .out3(demultiplexer_1_out3), .out4(demultiplexer_1_out4), .out5(demultiplexer_1_out5),
    .out6(demultiplexer_1_out6), .out7(demultiplexer_1_out7), .in(1'b1), .sel(ADDRES));  // open: en
  Exercicio04 _3 (
    .CLOCK(CLOCK), .R_W(R_W), .ADDRES(demultiplexer_1_out3), .CLR(CLEAR), ._input(\input ),
    ._output(_3__output));
  Exercicio04 _7 (
    .CLOCK(CLOCK), .R_W(CLOCK), .ADDRES(demultiplexer_1_out7), .CLR(CLEAR), ._input(\input ),
    ._output(_7__output));
  Exercicio04 _2 (
    .CLOCK(CLOCK), .R_W(R_W), .ADDRES(demultiplexer_1_out2), .CLR(CLEAR), ._input(\input ),
    ._output(_2__output));
  Exercicio04 _6 (
    .CLOCK(CLOCK), .R_W(CLOCK), .ADDRES(demultiplexer_1_out6), .CLR(CLEAR), ._input(\input ),
    ._output(_6__output));
  Exercicio04 _1 (
    .CLOCK(CLOCK), .R_W(R_W), .ADDRES(demultiplexer_1_out1), .CLR(CLEAR), ._input(\input ),
    ._output(_1__output));
  Exercicio04 _5 (
    .CLOCK(CLOCK), .R_W(CLOCK), .ADDRES(demultiplexer_1_out5), .CLR(CLEAR), ._input(\input ),
    ._output(_5__output));
  Exercicio04 _0 (
    .CLOCK(CLOCK), .R_W(R_W), .ADDRES(demultiplexer_1_out0), .CLR(CLEAR), ._input(\input ),
    ._output(_0__output));
  Exercicio04 _4 (
    .CLOCK(CLOCK), .R_W(CLOCK), .ADDRES(demultiplexer_1_out4), .CLR(CLEAR), ._input(\input ),
    ._output(_4__output));
  Multiplexer #(.select(3), .width(8)) multiplexer_1 (
    .in0(_0__output), .in1(_1__output), .in2(_2__output), .in3(_3__output), .in4(_4__output),
    .in5(_5__output), .in6(_6__output), .in7(_7__output), .out(\output ), .sel(ADDRES));  // open: en
endmodule
