// Logisim project Memória RAM 1x4.circ as structural Verilog: 1 circuit, main circuit main
module main (
  input  A,
  input  B,
  input  IN,
  input  R_W,
  output out_5
);

  wire and_1_out, and_2_out, and_3_out, and_4_out, and_5_out, and_6_out, and_7_out, and_8_out, and_9_out,
       and_10_out, and_11_out, and_12_out, and_13_out, and_14_out, and_15_out, and_16_out, j_k_ff_1_q,
       j_k_ff_2_q, j_k_ff_3_q, j_k_ff_4_q, not_1_out, not_2_out, not_3_out, not_4_out, not_5_out;

  not not_1 (not_1_out, A);
  not not_2 (not_2_out, B);
  and and_1 (and_1_out, not_1_out, not_2_out);
  not not_3 (not_3_out, IN);
  and and_2 (and_2_out, IN, and_1_out);
  and and_3 (and_3_out, not_3_out, and_1_out);
  not not_4 (not_4_out, A);
  and and_4 (and_4_out, not_4_out, B);
  and and_5 (and_5_out, and_1_out, j_k_ff_1_q);
  J_K_Flip_Flop j_k_ff_1 (.J(and_2_out), .clk(R_W), .K(and_3_out), .Q(j_k_ff_1_q));  // open: Qn, preset, en, reset
  and and_6 (and_6_out, IN, and_4_out);
  and and_7 (and_7_out, not_3_out, and_4_out);
  and and_8 (and_8_out, and_4_out, j_k_ff_2_q);
  J_K_Flip_Flop j_k_ff_2 (.J(and_6_out), .clk(R_W), .K(and_7_out), .Q(j_k_ff_2_q));  // open: Qn, preset, en, reset
  not not_5 (not_5_out, B);
  and and_9 (and_9_out, A, not_5_out);
  and and_10 (and_10_out, IN, and_9_out);
  J_K_Flip_Flop j_k_ff_3 (.J(and_10_out), .clk(R_W), .K(and_11_out), .Q(j_k_ff_3_q));  // open: Qn, preset, en, reset
  and and_11 (and_11_out, not_3_out, and_9_out);
  and and_12 (and_12_out, A, B);
  and and_13 (and_13_out, and_9_out, j_k_ff_3_q);
  and and_14 (and_14_out, IN, and_12_out);
  and and_15 (and_15_out, not_3_out, and_12_out);
  and and_16 (and_16_out, and_12_out, j_k_ff_4_q);
  J_K_Flip_Flop j_k_ff_4 (.J(and_14_out), .clk(R_W), .K(and_15_out), .Q(j_k_ff_4_q));  // open: Qn, preset, en, reset
  or or_1 (out_5, and_16_out, and_13_out, and_8_out, and_5_out);

  // Notes on the sheet:
  //   1 - escreve
  //   0 - lê
  //   Memória RAM 1x4
endmodule
