// Logisim project Memória RAM 1x8.circ as structural Verilog: 5 circuits, main circuit RAM 1x4
module RAM_1x4 (
  input  Addr,
  input  R_W,
  input  CLK,
  input  CLR,
  input  A,
  input  B,
  input  C,
  input  D,
  output out_9,
  output out_10,
  output out_11,
  output out_12
);

  wire and_1_out;

  and and_1 (and_1_out, Addr, R_W, CLK);
  J_K_Flip_Flop j_k_ff_1 (.J(A), .clk(and_1_out), .K(A), .Q(out_9), .reset(CLR));  // open: Qn, preset, en
  J_K_Flip_Flop j_k_ff_2 (.J(B), .clk(and_1_out), .K(B), .Q(out_10), .reset(CLR));  // open: Qn, preset, en
  J_K_Flip_Flop j_k_ff_3 (.J(C), .clk(and_1_out), .K(C), .Q(out_11), .reset(CLR));  // open: Qn, preset, en
  J_K_Flip_Flop j_k_ff_4 (.J(D), .clk(and_1_out), .K(D), .Q(out_12), .reset(CLR));  // open: Qn, preset, en

  // Notes on the sheet:
  //   Memória RAM 1x8
endmodule

module RAM_1x8 (
  input  A,
  input  B,
  input  C,
  input  D,
  input  E,
  input  F,
  input  G,
  input  H,
  input  Addr,
  input  R_W,
  input  CLK,
  input  CLR,
  output out_13,
  output out_14,
  output out_15,
  output out_16,
  output out_17,
  output out_18,
  output out_19,
  output out_20
);

  RAM_1x4 ram_1x4_1 (
    .Addr(Addr), .R_W(R_W), .CLK(CLK), .CLR(CLR), .A(A), .B(B), .C(C), .D(D), .out_9(out_13),
    .out_10(out_14), .out_11(out_15), .out_12(out_16));
  RAM_1x4 ram_1x4_2 (
    .Addr(Addr), .R_W(R_W), .CLK(CLK), .CLR(CLR), .A(E), .B(F), .C(G), .D(H), .out_9(out_17),
    .out_10(out_18), .out_11(out_19), .out_12(out_20));
endmodule

module RAM_4x8 (
  input  Addr,
  input  R_W,
  input  CLK,
  input  CLR,
  input  A,
  input  B,
  input  C,
  input  D,
  input  E,
  input  F,
  input  G,
  input  H,
  output out_13,
  output out_14,
  output out_15,
  output out_16,
  output out_17,
  output out_18,
  output out_19,
  output out_20,
  output out_21,
  output out_22,
  output out_23,
  output out_24,
  output out_25,
  output out_26,
  output out_27,
  output out_28,
  output out_29,
  output out_30,
  output out_31,
  output out_32,
  output out_33,
  output out_34,
  output out_35,
  output out_36,
  output out_37,
  output out_38,
  output out_39,
  output out_40,
  output out_41,
  output out_42,
  output out_43,
  output out_44
);

  RAM_1x8 ram_1x8_1 (
    .A(A), .B(B), .C(C), .D(D), .E(E), .F(F), .G(G), .H(H), .Addr(Addr), .R_W(R_W), .CLK(CLK), .CLR(CLR),
    .out_13(out_13), .out_14(out_14), .out_15(out_15), .out_16(out_16), .out_17(out_17), .out_18(out_18),
    .out_19(out_19), .out_20(out_20));
  RAM_1x8 ram_1x8_2 (
    .A(A), .B(B), .C(C), .D(D), .E(E), .F(F), .G(G), .H(H), .Addr(Addr), .R_W(R_W), .CLK(CLK), .CLR(CLR),
    .out_13(out_21), .out_14(out_22), .out_15(out_23), .out_16(out_24), .out_17(out_25), .out_18(out_26),
    .out_19(out_27), .out_20(out_28));
  RAM_1x8 ram_1x8_3 (
    .A(A), .B(B), .C(C), .D(D), .E(E), .F(F), .G(G), .H(H), .Addr(Addr), .R_W(R_W), .CLK(CLK), .CLR(CLR),
    .out_13(out_29), .out_14(out_30), .out_15(out_31), .out_16(out_32), .out_17(out_33), .out_18(out_34),
    .out_19(out_35), .out_20(out_36));
  RAM_1x8 ram_1x8_4 (
    .A(A), .B(B), .C(C), .D(D), .E(E), .F(F), .G(G), .H(H), .Addr(Addr), .R_W(R_W), .CLK(CLK), .CLR(CLR),
    .out_13(out_37), .out_14(out_38), .out_15(out_39), .out_16(out_40), .out_17(out_41), .out_18(out_42),
    .out_19(out_43), .out_20(out_44));
endmodule

module RAM_8x8 (
  input  Addr,
  input  R_W,
  input  CLK,
  input  CLR,
  input  A,
  input  B,
  input  C,
  input  D,
  input  E,
  input  F,
  input  G,
  input  H,
  output out_13,
  output out_14,
  output out_15,
  output out_16,
  output out_17,
  output out_18,
  output out_19,
  output out_20,
  output out_21,
  output out_22,
  output out_23,
  output out_24,
  output out_25,
  output out_26,
  output out_27,
  output out_28,
  output out_29,
  output out_30,
  output out_31,
  output out_32,
  output out_33,
  output out_34,
  output out_35,
  output out_36,
  output out_37,
  output out_38,
  output out_39,
  output out_40,
  output out_41,
  output out_42,
  output out_43,
  output out_44,
  output out_45,
  output out_46,
  output out_47,
  output out_48,
  output out_49,
  output out_50,
  output out_51,
  output out_52,
  output out_53,
  output out_54,
  output out_55,
  output out_56,
  output out_57,
  output out_58,
  output out_59,
  output out_60,
  output out_61,
  output out_62,
  output out_63,
  output out_64,
  output out_65,
  output out_66,
  output out_67,
  output out_68,
  output out_69,
  output out_70,
  output out_71,
  output out_72,
  output out_73,
  output out_74,
  output out_75,
  output out_76
);

  RAM_1x8 ram_1x8_1 (
    .A(A), .B(B), .C(C), .D(D), .E(E), .F(F), .G(G), .H(H), .Addr(Addr), .R_W(R_W), .CLK(CLK), .CLR(CLR),
    .out_13(out_13), .out_14(out_15), .out_15(out_17), .out_16(out_19), .out_17(out_21), .out_18(out_23),
    .out_19(out_25), .out_20(out_27));
  RAM_1x8 ram_1x8_2 (
    .A(A), .B(B), .C(C), .D(D), .E(E), .F(F), .G(G), .H(H), .Addr(Addr), .R_W(R_W), .CLK(CLK), .CLR(CLR),
    .out_13(out_29), .out_14(out_31), .out_15(out_33), .out_16(out_35), .out_17(out_37), .out_18(out_39),
    .out_19(out_41), .out_20(out_43));
  RAM_1x8 ram_1x8_3 (
    .A(A), .B(B), .C(C), .D(D), .E(E), .F(F), .G(G), .H(H), .Addr(Addr), .R_W(R_W), .CLK(CLK), .CLR(CLR),
    .out_13(out_45), .out_14(out_47), .out_15(out_49), .out_16(out_51), .out_17(out_53), .out_18(out_55),
    .out_19(out_57), .out_20(out_59));
  RAM_1x8 ram_1x8_4 (
    .A(A), .B(B), .C(C), .D(D), .E(E), .F(F), .G(G), .H(H), .Addr(Addr), .R_W(R_W), .CLK(CLK), .CLR(CLR),
    .out_13(out_61), .out_14(out_63), .out_15(out_65), .out_16(out_67), .out_17(out_69), .out_18(out_71),
    .out_19(out_73), .out_20(out_75));
  RAM_1x8 ram_1x8_5 (
    .A(A), .B(B), .C(C), .D(D), .E(E), .F(F), .G(G), .H(H), .Addr(Addr), .R_W(R_W), .CLK(CLK), .CLR(CLR),
    .out_13(out_14), .out_14(out_16), .out_15(out_18), .out_16(out_20), .out_17(out_22), .out_18(out_24),
    .out_19(out_26), .out_20(out_28));
  RAM_1x8 ram_1x8_6 (
    .A(A), .B(B), .C(C), .D(D), .E(E), .F(F), .G(G), .H(H), .Addr(Addr), .R_W(R_W), .CLK(CLK), .CLR(CLR),
    .out_13(out_30), .out_14(out_32), .out_15(out_34), .out_16(out_36), .out_17(out_38), .out_18(out_40),
    .out_19(out_42), .out_20(out_44));
  RAM_1x8 ram_1x8_7 (
    .A(A), .B(B), .C(C), .D(D), .E(E), .F(F), .G(G), .H(H), .Addr(Addr), .R_W(R_W), .CLK(CLK), .CLR(CLR),
    .out_13(out_46), .out_14(out_48), .out_15(out_50), .out_16(out_52), .out_17(out_54), .out_18(out_56),
    .out_19(out_58), .out_20(out_60));
  RAM_1x8 ram_1x8_8 (
    .A(A), .B(B), .C(C), .D(D), .E(E), .F(F), .G(G), .H(H), .Addr(Addr), .R_W(R_W), .CLK(CLK), .CLR(CLR),
    .out_13(out_62), .out_14(out_64), .out_15(out_66), .out_16(out_68), .out_17(out_70), .out_18(out_72),
    .out_19(out_74), .out_20(out_76));
endmodule

module RAM_1x16 (
  input  Addr,
  input  R_W,
  input  CLK,
  input  CLR,
  input  A,
  input  B,
  input  C,
  input  D,
  output out_9,
  output out_10,
  output out_11,
  output out_12,
  output out_13,
  output out_14,
  output out_15,
  output out_16,
  output out_17,
  output out_18,
  output out_19,
  output out_20,
  output out_21,
  output out_22,
  output out_23,
  output out_24
);

  RAM_1x4 ram_1x4_1 (
    .Addr(Addr), .R_W(R_W), .CLK(CLK), .CLR(CLR), .A(A), .B(B), .C(C), .D(D), .out_9(out_9), .out_10(out_10),
    .out_11(out_11), .out_12(out_12));
  RAM_1x4 ram_1x4_2 (
    .Addr(Addr), .R_W(R_W), .CLK(CLK), .CLR(CLR), .A(A), .B(B), .C(C), .D(D), .out_9(out_13),
    .out_10(out_14), .out_11(out_15), .out_12(out_16));
  RAM_1x4 ram_1x4_3 (
    .Addr(Addr), .R_W(R_W), .CLK(CLK), .CLR(CLR), .A(A), .B(B), .C(C), .D(D), .out_9(out_17),
    .out_10(out_18), .out_11(out_19), .out_12(out_20));
  RAM_1x4 ram_1x4_4 (
    .Addr(Addr), .R_W(R_W), .CLK(CLK), .CLR(CLR), .A(A), .B(B), .C(C), .D(D), .out_9(out_21),
    .out_10(out_22), .out_11(out_23), .out_12(out_24));
endmodule
