// Logisim project Exercicio001.circ as structural Verilog: 3 circuits, main circuit main
module main (
  input  address,
  input  R_W,
  input  CLK,
  input  [3:0] \input ,
  input  CLR,
  output [3:0] \output 
);

  _1x4 u_1x4_1 (.address(address), .R_W(R_W), .CLK(CLK), .\input (\input ), .CLR(CLR), .\output (\output ));
endmodule

module _1x1 (
  input  address,
  input  R_W,
  input  CLK,
  input  IN,
  input  CLR,
  output \output 
);

  wire and_1_out, j_k_ff_1_q;

  and and_1 (and_1_out, address, R_W, CLK);
  J_K_Flip_Flop j_k_ff_1 (.J(IN), .clk(and_1_out), .K(IN), .Q(j_k_ff_1_q), .reset(CLR));  // open: Qn, preset, en
  and and_2 (\output , address, j_k_ff_1_q);
endmodule

// RAM
module _1x4 (
  input  address,
  input  R_W,
  input  CLK,
  input  [3:0] \input ,
  input  CLR,
  output [3:0] \output 
);

  _1x1 u_1x1_1 (.address(address), .R_W(R_W), .CLK(CLK), .IN(\input [0]), .CLR(CLR), .\output (\output [0]));
  _1x1 u_1x1_2 (.address(address), .R_W(R_W), .CLK(CLK), .IN(\input [1]), .CLR(CLR), .\output (\output [1]));
  _1x1 u_1x1_3 (.address(address), .R_W(R_W), .CLK(CLK), .IN(\input [2]), .CLR(CLR), .\output (\output [2]));
  _1x1 u_1x1_4 (.address(address), .R_W(R_W), .CLK(CLK), .IN(\input [3]), .CLR(CLR), .\output (\output [3]));
endmodule
