// Logisim project Exercicio002.circ as structural Verilog: 4 circuits, main circuit main
module main (
  input  address,
  input  R_W,
  input  CLK,
  input  [7:0] IN,
  input  CLR,
  output [7:0] OUT
);

  _1x8 u_1x8_1 (.address(address), .R_W(R_W), .CLK(CLK), .IN(IN), .CLR(CLR), .OUT(OUT));
endmodule

module _1x1 (
  input  address,
  input  R_W,
  input  CLK,
  input  IN,
  input  CLR,
  output out_6
);

  wire and_1_out, j_k_ff_1_q;

  and and_1 (and_1_out, address, R_W, CLK);
  J_K_Flip_Flop j_k_ff_1 (.J(IN), .clk(and_1_out), .K(IN), .Q(j_k_ff_1_q), .reset(CLR));  // open: Qn, preset, en
  and and_2 (out_6, address, j_k_ff_1_q);
endmodule

module _1x4 (
  input  address,
  input  R_W,
  input  CLK,
  input  [3:0] \input ,
  input  CLR,
  output [3:0] \output 
);

  _1x1 u_1x1_1 (.address(address), .R_W(R_W), .CLK(CLK), .IN(\input [0]), .CLR(CLR), .out_6(\output [0]));
  _1x1 u_1x1_2 (.address(address), .R_W(R_W), .CLK(CLK), .IN(\input [1]), .CLR(CLR), .out_6(\output [1]));
  _1x1 u_1x1_3 (.address(address), .R_W(R_W), .CLK(CLK), .IN(\input [2]), .CLR(CLR), .out_6(\output [2]));
  _1x1 u_1x1_4 (.address(address), .R_W(R_W), .CLK(CLK), .IN(\input [3]), .CLR(CLR), .out_6(\output [3]));
endmodule

// RAM
module _1x8 (
  input  address,
  input  R_W,
  input  CLK,
  input  CLR,
  input  [7:0] IN,
  output [7:0] OUT
);

  _1x4 u_1x4_1 (.address(address), .R_W(R_W), .CLK(CLK), .\input (IN[3:0]), .CLR(CLR), .\output (OUT[3:0]));
  _1x4 u_1x4_2 (.address(address), .R_W(R_W), .CLK(CLK), .\input (IN[7:4]), .CLR(CLR), .\output (OUT[7:4]));
endmodule
