// Logisim project Exercicio003.circ as structural Verilog: 6 circuits, main circuit main
module main (
  input  [31:0] IN,
  input  [1:0] address,
  input  R_W,
  input  CLR,
  input  CLK,
  output [31:0] OUT
);

  _4x8_2 u_4x8_2_1 (.IN(IN), .address(address), .R_W(R_W), .CLK(CLK), .CLR(CLR), .OUT(OUT));
endmodule

module _1x1 (
  input  address,
  input  R_W,
  input  CLK,
  input  IN,
  input  CLR,
  output out_6
);

  wire and_1_out, j_k_ff_1_q;

  and and_1 (and_1_out, address, R_W, CLK);
  J_K_Flip_Flop j_k_ff_1 (.J(IN), .clk(and_1_out), .K(IN), .Q(j_k_ff_1_q), .reset(CLR));  // open: Qn, preset, en
  and and_2 (out_6, address, j_k_ff_1_q);
endmodule

module _1x4 (
  input  address,
  input  R_W,
  input  CLK,
  input  [3:0] \input ,
  input  CLR,
  output [3:0] \output 
);

  _1x1 u_1x1_1 (.address(address), .R_W(R_W), .CLK(CLK), .IN(\input [0]), .CLR(CLR), .out_6(\output [0]));
  _1x1 u_1x1_2 (.address(address), .R_W(R_W), .CLK(CLK), .IN(\input [1]), .CLR(CLR), .out_6(\output [1]));
  _1x1 u_1x1_3 (.address(address), .R_W(R_W), .CLK(CLK), .IN(\input [2]), .CLR(CLR), .out_6(\output [2]));
  _1x1 u_1x1_4 (.address(address), .R_W(R_W), .CLK(CLK), .IN(\input [3]), .CLR(CLR), .out_6(\output [3]));
endmodule

// 1X8
module _1x8 (
  input  address,
  input  R_W,
  input  CLK,
  input  CLR,
  input  [7:0] IN,
  output [7:0] OUT
);

  _1x4 u_1x4_1 (.address(address), .R_W(R_W), .CLK(CLK), .\input (IN[3:0]), .CLR(CLR), .\output (OUT[3:0]));
  _1x4 u_1x4_2 (.address(address), .R_W(R_W), .CLK(CLK), .\input (IN[7:4]), .CLR(CLR), .\output (OUT[7:4]));
endmodule

// RAM
module _4x8 (
  input  [31:0] IN,
  input  address,
  input  R_W,
  input  CLK,
  input  CLR,
  output [31:0] OUT
);

  _1x8 u_1x8_1 (.address(address), .R_W(R_W), .CLK(CLK), .IN(IN[7:0]), .CLR(CLR), .OUT(OUT[7:0]));
  _1x8 u_1x8_2 (.address(address), .R_W(R_W), .CLK(CLK), .IN(IN[15:8]), .CLR(CLR), .OUT(OUT[15:8]));
  _1x8 u_1x8_3 (.address(address), .R_W(R_W), .CLK(CLK), .IN(IN[23:16]), .CLR(CLR), .OUT(OUT[23:16]));
  _1x8 u_1x8_4 (.address(address), .R_W(R_W), .CLK(CLK), .IN(IN[31:24]), .CLR(CLR), .OUT(OUT[31:24]));
endmodule

// RAM
module _4x8_2 (
  input  [31:0] IN,
  input  [1:0] address,
  input  R_W,
  input  CLK,
  input  CLR,
  output [31:0] OUT
);

  wire demultiplexer_1_out0, demultiplexer_1_out1, demultiplexer_1_out2, demultiplexer_1_out3;
  wire [7:0] n1x8_1_out, n1x8_2_out, n1x8_3_out;
  wire [15:8] n1x8_4_out;

  _1x8 u_1x8_1 (.address(demultiplexer_1_out0), .R_W(R_W), .CLK(CLK), .IN(IN[7:0]), .CLR(CLR), .OUT(n1x8_1_out));
  Demultiplexer #(.select(2)) demultiplexer_1 (
    .out0(demultiplexer_1_out0), .out1(demultiplexer_1_out1), .out2(demultiplexer_1_out2),
    .out3(demultiplexer_1_out3), .in(1'b1), .sel(address));  // open: en
  _1x8 u_1x8_2 (.address(demultiplexer_1_out1), .R_W(R_W), .CLK(CLK), .IN(IN[15:8]), .CLR(CLR), .OUT(n1x8_2_out));
  _1x8 u_1x8_3 (.address(demultiplexer_1_out2), .R_W(R_W), .CLK(CLK), .IN(IN[23:16]), .CLR(CLR), .OUT(n1x8_3_out));
  _1x8 u_1x8_4 (.address(demultiplexer_1_out3), .R_W(R_W), .CLK(CLK), .IN(IN[31:24]), .CLR(CLR), .OUT(n1x8_4_out));
  Multiplexer #(.width(16)) multiplexer_1 (
    .in0({n1x8_2_out, n1x8_1_out}), .in1({n1x8_4_out, n1x8_3_out}), .out(OUT[15:0]), .sel(address[0]));  // open: en
  Multiplexer #(.width(16)) multiplexer_2 (
    .in0({n1x8_4_out, n1x8_3_out}), .in1({n1x8_2_out, n1x8_1_out}), .out(OUT[31:16]), .sel(address[1]));  // open: en
endmodule
