// Logisim project Exercicio004.circ as structural Verilog: 2 circuits, main circuit main
module main (
  input  address,
  input  R_W,
  input  CLK,
  input  [7:0] IN,
  input  CLR,
  output [7:0] OUT
);

  _1X8_JK u_1x8_jk_1 (.address(address), .R_W(R_W), .CLK(CLK), .IN(IN), .CLR(CLR), .OUT(OUT));
endmodule

// RAM
module _1X8_JK (
  input  address,
  input  R_W,
  input  CLK,
  input  [7:0] IN,
  input  CLR,
  output [7:0] OUT
);

  wire and_1_out, j_k_ff_1_q, j_k_ff_2_q, j_k_ff_3_q, j_k_ff_4_q, j_k_ff_5_q, j_k_ff_6_q, j_k_ff_7_q,
       j_k_ff_8_q;

  and and_1 (and_1_out, address, R_W, CLK);
  J_K_Flip_Flop j_k_ff_1 (.J(IN[0]), .clk(and_1_out), .K(IN[0]), .Q(j_k_ff_1_q), .reset(CLR));  // open: Qn, preset, en
  and and_2 (OUT[0], address, j_k_ff_1_q);
  J_K_Flip_Flop j_k_ff_2 (.J(IN[1]), .clk(and_1_out), .K(IN[1]), .Q(j_k_ff_2_q), .reset(CLR));  // open: Qn, preset, en
  and and_3 (OUT[1], address, j_k_ff_2_q);
  J_K_Flip_Flop j_k_ff_3 (.J(IN[2]), .clk(and_1_out), .K(IN[2]), .Q(j_k_ff_3_q), .reset(CLR));  // open: Qn, preset, en
  and and_4 (OUT[2], address, j_k_ff_3_q);
  J_K_Flip_Flop j_k_ff_4 (.J(IN[3]), .clk(and_1_out), .K(IN[3]), .Q(j_k_ff_4_q), .reset(CLR));  // open: Qn, preset, en
  and and_5 (OUT[3], address, j_k_ff_4_q);
  J_K_Flip_Flop j_k_ff_5 (.J(IN[4]), .clk(and_1_out), .K(IN[4]), .Q(j_k_ff_5_q), .reset(CLR));  // open: Qn, preset, en
  and and_6 (OUT[4], address, j_k_ff_5_q);
  J_K_Flip_Flop j_k_ff_6 (.J(IN[5]), .clk(and_1_out), .K(IN[5]), .Q(j_k_ff_6_q), .reset(CLR));  // open: Qn, preset, en
  and and_7 (OUT[5], address, j_k_ff_6_q);
  J_K_Flip_Flop j_k_ff_7 (.J(IN[6]), .clk(and_1_out), .K(IN[6]), .Q(j_k_ff_7_q), .reset(CLR));  // open: Qn, preset, en
  and and_8 (OUT[6], address, j_k_ff_7_q);
  J_K_Flip_Flop j_k_ff_8 (.J(IN[7]), .clk(and_1_out), .K(IN[7]), .Q(j_k_ff_8_q), .reset(CLR));  // open: Qn, preset, en
  and and_9 (OUT[7], address, j_k_ff_8_q);
endmodule
