// Logisim project Exercicio005.circ as structural Verilog: 3 circuits, main circuit main
module main (
  input  address,
  input  R_W,
  input  CLK,
  input  [31:0] in_4,
  input  [31:0] in_5,
  input  in_6,
  output [31:0] out_7,
  output [31:0] out_8
);

  _8x8_JK u_8x8_jk_1 (
    .address(address), .R_W(R_W), .CLK(CLK), .IN(in_4), .in_5(in_5), .CLR(in_6), .OUT(out_7), .out_8(out_8));
endmodule

// 1x8 JK
module _1X8_JK (
  input  address,
  input  R_W,
  input  CLK,
  input  [7:0] IN,
  input  CLR,
  output [7:0] OUT
);

  wire and_1_out, j_k_ff_1_q, j_k_ff_2_q, j_k_ff_3_q, j_k_ff_4_q, j_k_ff_5_q, j_k_ff_6_q, j_k_ff_7_q,
       j_k_ff_8_q;

  and and_1 (and_1_out, address, R_W, CLK);
  J_K_Flip_Flop j_k_ff_1 (.J(IN[0]), .clk(and_1_out), .K(IN[0]), .Q(j_k_ff_1_q), .reset(CLR));  // open: Qn, preset, en
  and and_2 (OUT[0], address, j_k_ff_1_q);
  J_K_Flip_Flop j_k_ff_2 (.J(IN[1]), .clk(and_1_out), .K(IN[1]), .Q(j_k_ff_2_q), .reset(CLR));  // open: Qn, preset, en
  and and_3 (OUT[1], address, j_k_ff_2_q);
  J_K_Flip_Flop j_k_ff_3 (.J(IN[2]), .clk(and_1_out), .K(IN[2]), .Q(j_k_ff_3_q), .reset(CLR));  // open: Qn, preset, en
  and and_4 (OUT[2], address, j_k_ff_3_q);
  J_K_Flip_Flop j_k_ff_4 (.J(IN[3]), .clk(and_1_out), .K(IN[3]), .Q(j_k_ff_4_q), .reset(CLR));  // open: Qn, preset, en
  and and_5 (OUT[3], address, j_k_ff_4_q);
  J_K_Flip_Flop j_k_ff_5 (.J(IN[4]), .clk(and_1_out), .K(IN[4]), .Q(j_k_ff_5_q), .reset(CLR));  // open: Qn, preset, en
  and and_6 (OUT[4], address, j_k_ff_5_q);
  J_K_Flip_Flop j_k_ff_6 (.J(IN[5]), .clk(and_1_out), .K(IN[5]), .Q(j_k_ff_6_q), .reset(CLR));  // open: Qn, preset, en
  and and_7 (OUT[5], address, j_k_ff_6_q);
  J_K_Flip_Flop j_k_ff_7 (.J(IN[6]), .clk(and_1_out), .K(IN[6]), .Q(j_k_ff_7_q), .reset(CLR));  // open: Qn, preset, en
  and and_8 (OUT[6], address, j_k_ff_7_q);
  J_K_Flip_Flop j_k_ff_8 (.J(IN[7]), .clk(and_1_out), .K(IN[7]), .Q(j_k_ff_8_q), .reset(CLR));  // open: Qn, preset, en
  and and_9 (OUT[7], address, j_k_ff_8_q);
endmodule

// RAM
module _8x8_JK (
  input  address,
  input  R_W,
  input  CLK,
  input  [31:0] IN,
  input  [31:0] in_5,
  input  CLR,
  output [31:0] OUT,
  output [31:0] out_8
);

  _1X8_JK u_1x8_jk_1 (.address(address), .R_W(R_W), .CLK(CLK), .IN(IN[7:0]), .CLR(CLR), .OUT(OUT[7:0]));
  _1X8_JK u_1x8_jk_2 (.address(address), .R_W(R_W), .CLK(CLK), .IN(IN[15:8]), .CLR(CLR), .OUT(OUT[15:8]));
  _1X8_JK u_1x8_jk_3 (.address(address), .R_W(R_W), .CLK(CLK), .IN(IN[23:16]), .CLR(CLR), .OUT(OUT[23:16]));
  _1X8_JK u_1x8_jk_4 (.address(address), .R_W(R_W), .CLK(CLK), .IN(IN[31:24]), .CLR(CLR), .OUT(OUT[31:24]));
  _1X8_JK u_1x8_jk_5 (.address(address), .R_W(R_W), .CLK(CLK), .IN(in_5[7:0]), .CLR(CLR), .OUT(out_8[7:0]));
  _1X8_JK u_1x8_jk_6 (.address(address), .R_W(R_W), .CLK(CLK), .IN(in_5[15:8]), .CLR(CLR), .OUT(out_8[15:8]));
  _1X8_JK u_1x8_jk_7 (.address(address), .R_W(R_W), .CLK(CLK), .IN(in_5[23:16]), .CLR(CLR), .OUT(out_8[23:16]));
  _1X8_JK u_1x8_jk_8 (.address(address), .R_W(R_W), .CLK(CLK), .IN(in_5[31:24]), .CLR(CLR), .OUT(out_8[31:24]));
endmodule
