// Logisim project Circuitos.circ as structural Verilog: 5 circuits, main circuit main
module main (
  input  Addr,
  input  R_W,
  input  IN_0,
  input  CLR,
  input  IN_1,
  input  IN_2,
  input  IN_3,
  output s1,
  output s2,
  output s3,
  output s4
);

  wire and_1_out, clock_1_out, j_k_ff_1_q, j_k_ff_2_q, j_k_ff_3_q, j_k_ff_4_q;

  Clock clock_1 (.out(clock_1_out));
  and and_1 (and_1_out, Addr, R_W, clock_1_out);
  J_K_Flip_Flop j_k_ff_1 (.J(IN_0), .clk(and_1_out), .K(IN_0), .Q(j_k_ff_1_q), .reset(CLR));  // open: Qn, preset, en
  J_K_Flip_Flop j_k_ff_2 (.J(IN_1), .clk(and_1_out), .K(IN_1), .Q(j_k_ff_2_q), .reset(CLR));  // open: Qn, preset, en
  J_K_Flip_Flop j_k_ff_3 (.J(IN_2), .clk(and_1_out), .K(IN_2), .Q(j_k_ff_3_q), .reset(CLR));  // open: Qn, preset, en
  J_K_Flip_Flop j_k_ff_4 (.J(IN_3), .clk(and_1_out), .K(IN_3), .Q(j_k_ff_4_q), .reset(CLR));  // open: Qn, preset, en
  and and_2 (s1, j_k_ff_1_q, Addr);
  and and_3 (s2, j_k_ff_2_q, Addr);
  and and_4 (s3, j_k_ff_3_q, Addr);
  and and_5 (s4, j_k_ff_4_q, Addr);

  // Notes on the sheet:
  //   CLK
  //   Memória RAM 1x4
endmodule

module Exercicio02 (
  input  Addr,
  input  R_W,
  input  CLK,
  input  IN0,
  input  IN1,
  input  IN2,
  input  IN3,
  input  IN4,
  input  IN5,
  input  IN6,
  input  IN7,
  output s0,
  output s1,
  output s2,
  output s3,
  output s4,
  output s5,
  output s6,
  output s7
);

  main main_1 (
    .Addr(Addr), .R_W(R_W), .IN_0(CLK), .CLR(IN0), .IN_1(IN1), .IN_2(IN2), .IN_3(IN3), .s1(s0), .s2(s1),
    .s3(s2), .s4(s3));
  main main_2 (
    .Addr(Addr), .R_W(R_W), .IN_0(CLK), .CLR(IN4), .IN_1(IN5), .IN_2(IN6), .IN_3(IN7), .s1(s4), .s2(s5),
    .s3(s6), .s4(s7));

  // Notes on the sheet:
  //   Memória RAM 1x8
endmodule

module Exercicio03 (
  input  Addr,
  input  R_W,
  input  CLK,
  input  IN0,
  input  IN1,
  input  IN2,
  input  IN3,
  input  IN4,
  input  IN5,
  input  IN6,
  input  IN7,
  output s2,
  output s0,
  output s1,
  output s3,
  output s4,
  output s5,
  output s6,
  output s7,
  output s8,
  output s9,
  output s10,
  output s12,
  output s13,
  output s14,
  output s15,
  output s11,
  output s16,
  output s17,
  output s18,
  output s20,
  output s21,
  output s22,
  output s23,
  output s19,
  output s24,
  output s25,
  output s26,
  output s28,
  output s29,
  output s30,
  output s31,
  output s27
);

  Exercicio02 exercicio02_1 (
    .Addr(Addr), .R_W(R_W), .CLK(CLK), .IN0(IN0), .IN1(IN1), .IN2(IN2), .IN3(IN2), .IN4(IN2), .IN5(IN2),
    .IN6(IN2), .IN7(IN7), .s3(s3), .s0(s0), .s1(s1), .s2(s2), .s4(s4), .s5(s5), .s6(s6), .s7(s7));
  Exercicio02 exercicio02_2 (
    .Addr(Addr), .R_W(R_W), .CLK(CLK), .IN0(IN0), .IN1(IN1), .IN2(IN2), .IN3(IN7), .IN4(IN2), .IN5(IN2),
    .IN6(IN2), .IN7(IN7), .s3(s11), .s0(s8), .s1(s9), .s2(s10), .s4(s12), .s5(s13), .s6(s14), .s7(s15));
  Exercicio02 exercicio02_3 (
    .Addr(Addr), .R_W(R_W), .CLK(CLK), .IN0(IN0), .IN1(IN1), .IN2(IN2), .IN3(IN2), .IN4(IN2), .IN5(IN2),
    .IN6(IN2), .IN7(IN7), .s3(s19), .s0(s16), .s1(s17), .s2(s18), .s4(s20), .s5(s21), .s6(s22), .s7(s23));
  Exercicio02 exercicio02_4 (
    .Addr(Addr), .R_W(R_W), .CLK(CLK), .IN0(IN0), .IN1(IN1), .IN2(IN2), .IN3(IN2), .IN4(IN2), .IN5(IN2),
    .IN6(IN2), .IN7(IN7), .s3(s27), .s0(s24), .s1(s25), .s2(s26), .s4(s28), .s5(s29), .s6(s30), .s7(s31));

  assign IN3 = IN2;
  assign IN4 = IN2;
  assign IN5 = IN2;
  assign IN6 = IN2;

  // Notes on the sheet:
  //   Memória Ram 4x8
endmodule

module Exercicio04 (
  input  Addr,
  input  R_W,
  input  IN_0,
  input  CLR,
  input  IN_1,
  input  IN_2,
  input  IN_3,
  input  In_4,
  input  In_5,
  input  IN_6,
  input  IN_7,
  output s0,
  output s1,
  output s2,
  output s3,
  output s4,
  output s5,
  output s6,
  output s7
);

  wire and_1_out, clock_1_out, j_k_ff_1_q, j_k_ff_2_q, j_k_ff_3_q, j_k_ff_4_q, j_k_ff_5_q, j_k_ff_6_q,
       j_k_ff_7_q, j_k_ff_8_q;

  Clock clock_1 (.out(clock_1_out));
  and and_1 (and_1_out, Addr, R_W, clock_1_out);
  J_K_Flip_Flop j_k_ff_1 (.J(IN_0), .clk(and_1_out), .K(IN_0), .Q(j_k_ff_1_q), .reset(CLR));  // open: Qn, preset, en
  J_K_Flip_Flop j_k_ff_2 (.J(IN_1), .clk(and_1_out), .K(IN_1), .Q(j_k_ff_2_q), .reset(CLR));  // open: Qn, preset, en
  J_K_Flip_Flop j_k_ff_3 (.J(IN_2), .clk(and_1_out), .K(IN_2), .Q(j_k_ff_3_q), .reset(CLR));  // open: Qn, preset, en
  J_K_Flip_Flop j_k_ff_4 (.J(IN_3), .clk(and_1_out), .K(IN_3), .Q(j_k_ff_4_q), .reset(CLR));  // open: Qn, preset, en
  J_K_Flip_Flop j_k_ff_5 (.J(In_4), .clk(and_1_out), .K(In_4), .Q(j_k_ff_5_q));  // open: Qn, preset, en, reset
  J_K_Flip_Flop j_k_ff_6 (.J(In_5), .clk(and_1_out), .K(In_5), .Q(j_k_ff_6_q));  // open: Qn, preset, en, reset
  J_K_Flip_Flop j_k_ff_7 (.J(IN_6), .clk(and_1_out), .K(IN_6), .Q(j_k_ff_7_q));  // open: Qn, preset, en, reset
  J_K_Flip_Flop j_k_ff_8 (.J(IN_7), .clk(and_1_out), .K(IN_7), .Q(j_k_ff_8_q));  // open: Qn, preset, en, reset
  and and_2 (s0, j_k_ff_1_q, Addr);
  and and_3 (s1, j_k_ff_2_q, Addr);
  and and_4 (s2, j_k_ff_3_q, Addr);
  and and_5 (s3, j_k_ff_4_q, Addr);
  and and_6 (s4, j_k_ff_5_q, Addr);
  and and_7 (s5, j_k_ff_6_q, Addr);
  and and_8 (s6, Addr, j_k_ff_7_q);
  and and_9 (s7, Addr, j_k_ff_8_q, j_k_ff_8_q);

  // Notes on the sheet:
  //   Mémoria RAM 1x8
endmodule

module Exercicio_05 (
  input  Addr,
  input  R_W,
  input  CLK,
  input  IN0,
  input  IN1,
  input  IN2,
  input  IN3,
  input  IN4,
  input  IN5,
  input  IN6,
  input  IN7,
  output s0,
  output s1,
  output s2,
  output s3,
  output s4,
  output s5,
  output s5_2,
  output s6,
  output s0_2,
  output out_21,
  output out_22,
  output out_23,
  output out_24,
  output out_25,
  output out_26,
  output out_27,
  output out_28,
  output out_29,
  output out_30,
  output out_31,
  output out_32,
  output out_33,
  output out_34,
  output out_35,
  output out_36,
  output out_37,
  output out_38,
  output out_39,
  output out_40,
  output out_41,
  output out_42,
  output out_43,
  output out_44,
  output out_45,
  output out_46,
  output out_47,
  output out_48,
  output out_49,
  output out_50,
  output out_51,
  output out_52,
  output out_53,
  output out_54,
  output out_55,
  output out_56,
  output out_57,
  output out_58,
  output out_59,
  output out_60,
  output out_61,
  output out_62,
  output out_63,
  output out_64,
  output out_65,
  output out_66,
  output out_67,
  output out_68,
  output out_69,
  output out_70,
  output out_71,
  output out_72,
  output out_73,
  output out_74,
  output out_75
);

  Exercicio04 exercicio04_1 (
    .Addr(Addr), .R_W(R_W), .IN_0(CLK), .CLR(IN0), .IN_1(IN1), .IN_2(IN2), .IN_3(IN3), .In_4(IN4),
    .In_5(IN5), .IN_6(IN6), .IN_7(IN7), .s0(s0), .s1(s1), .s2(s2), .s3(s3), .s4(s4), .s5(s5), .s6(s5_2),
    .s7(s6));
  Exercicio04 exercicio04_2 (
    .Addr(Addr), .R_W(CLK), .IN_0(IN0), .CLR(IN1), .IN_1(R_W), .IN_2(IN2), .IN_3(IN3), .In_4(IN4),
    .In_5(IN5), .IN_6(IN6), .IN_7(IN7), .s0(s0_2), .s1(out_21), .s2(out_22), .s3(out_23), .s4(out_24),
    .s5(out_25), .s6(out_26), .s7(out_27));
  Exercicio04 exercicio04_3 (
    .Addr(Addr), .R_W(CLK), .IN_0(IN0), .CLR(IN1), .IN_1(R_W), .IN_2(IN2), .IN_3(IN3), .In_4(IN4),
    .In_5(IN5), .IN_6(IN6), .IN_7(IN7), .s0(out_28), .s1(out_29), .s2(out_30), .s3(out_31), .s4(out_32),
    .s5(out_33), .s6(out_34), .s7(out_35));
  Exercicio04 exercicio04_4 (
    .Addr(Addr), .R_W(CLK), .IN_0(IN0), .CLR(IN1), .IN_1(R_W), .IN_2(IN2), .IN_3(IN3), .In_4(IN4),
    .In_5(IN5), .IN_6(IN6), .IN_7(IN7), .s0(out_36), .s1(out_37), .s2(out_38), .s3(out_39), .s4(out_40),
    .s5(out_41), .s6(out_42), .s7(out_43));
  Exercicio04 exercicio04_5 (
    .Addr(Addr), .R_W(CLK), .IN_0(IN0), .CLR(IN1), .IN_1(R_W), .IN_2(IN2), .IN_3(IN3), .In_4(IN4),
    .In_5(IN5), .IN_6(IN6), .IN_7(IN7), .s0(out_44), .s1(out_45), .s2(out_46), .s3(out_47), .s4(out_48),
    .s5(out_49), .s6(out_50), .s7(out_51));
  Exercicio04 exercicio04_6 (
    .Addr(Addr), .R_W(CLK), .IN_0(IN0), .CLR(IN1), .IN_1(R_W), .IN_2(IN2), .IN_3(IN3), .In_4(IN4),
    .In_5(IN5), .IN_6(IN6), .IN_7(IN7), .s0(out_52), .s1(out_53), .s2(out_54), .s3(out_55), .s4(out_56),
    .s5(out_57), .s6(out_58), .s7(out_59));
  Exercicio04 exercicio04_7 (
    .Addr(Addr), .R_W(CLK), .IN_0(IN0), .CLR(IN1), .IN_1(R_W), .IN_2(IN2), .IN_3(IN3), .In_4(IN4),
    .In_5(IN5), .IN_6(IN6), .IN_7(IN7), .s0(out_60), .s1(out_61), .s2(out_62), .s3(out_63), .s4(out_64),
    .s5(out_65), .s6(out_66), .s7(out_67));
  Exercicio04 exercicio04_8 (
    .Addr(Addr), .R_W(CLK), .IN_0(IN0), .CLR(IN1), .IN_1(R_W), .IN_2(IN2), .IN_3(IN3), .In_4(IN4),
    .In_5(IN5), .IN_6(IN6), .IN_7(IN7), .s0(out_68), .s1(out_69), .s2(out_70), .s3(out_71), .s4(out_72),
    .s5(out_73), .s6(out_74), .s7(out_75));

  // Notes on the sheet:
  //   Mémoria RAM 8x8
endmodule
