// Logisim project guia10.circ as structural Verilog: 5 circuits, main circuit RAM 1X4
// 1X4
module RAM_1X4 (
  input  ADDR,
  input  CLK,
  input  R_W,
  input  [3:0] INPUT,
  input  CLR,
  output [3:0] OUT
);

  wire and_1_out, j_k_ff_1_q, j_k_ff_2_q, j_k_ff_3_q, j_k_ff_4_q, not_1_out, not_2_out, not_3_out, not_4_out;

  and and_1 (and_1_out, CLK, R_W, ADDR);
  not not_1 (not_1_out, INPUT[0]);
  not not_2 (not_2_out, INPUT[1]);
  J_K_Flip_Flop j_k_ff_1 (
    .J(INPUT[0]), .clk(and_1_out), .K(not_1_out), .Q(j_k_ff_1_q), .reset(CLR));  // open: Qn, preset, en
  J_K_Flip_Flop j_k_ff_2 (
    .J(INPUT[1]), .clk(and_1_out), .K(not_2_out), .Q(j_k_ff_2_q), .reset(CLR));  // open: Qn, preset, en
  not not_3 (not_3_out, INPUT[2]);
  and and_2 (OUT[0], ADDR, j_k_ff_1_q);
  and and_3 (OUT[1], ADDR, j_k_ff_2_q);
  and and_4 (OUT[2], ADDR, j_k_ff_3_q);
  J_K_Flip_Flop j_k_ff_3 (
    .J(INPUT[2]), .clk(and_1_out), .K(not_3_out), .Q(j_k_ff_3_q), .reset(CLR));  // open: Qn, preset, en
  J_K_Flip_Flop j_k_ff_4 (
    .J(INPUT[3]), .clk(and_1_out), .K(not_4_out), .Q(j_k_ff_4_q), .reset(CLR));  // open: Qn, preset, en
  not not_4 (not_4_out, INPUT[3]);
  and and_5 (OUT[3], ADDR, j_k_ff_4_q);
endmodule

// 1X8
module RAM_1X8 (
  input  ADDR,
  input  CLK,
  input  [7:0] INPUT,
  input  R_W,
  input  CLR,
  output [7:0] OUT
);

  RAM_1X4 ram_1x4_1 (.ADDR(ADDR), .R_W(R_W), .OUT(OUT[3:0]), .INPUT(INPUT[3:0]), .CLR(CLR), .CLK(CLK));
  RAM_1X4 ram_1x4_2 (.ADDR(ADDR), .R_W(R_W), .OUT(OUT[7:4]), .INPUT(INPUT[7:4]), .CLR(CLR), .CLK(CLK));
endmodule

module RAM_4X8 (
  input  [1:0] ADDR,
  input  CLK,
  input  [7:0] INPUT,
  input  R_W,
  input  CLR,
  output [7:0] OUT
);

  wire demultiplexer_1_out0, demultiplexer_1_out1, demultiplexer_1_out2, demultiplexer_1_out3;
  wire [7:0] ram_1x8_1_out, ram_1x8_2_out, ram_1x8_3_out, ram_1x8_4_out;

  Demultiplexer #(.select(2)) demultiplexer_1 (
    .out0(demultiplexer_1_out0), .out1(demultiplexer_1_out1), .out2(demultiplexer_1_out2),
    .out3(demultiplexer_1_out3), .in(1'b1), .sel(ADDR));  // open: en
  RAM_1X8 ram_1x8_1 (.ADDR(demultiplexer_1_out0), .CLK(R_W), .R_W(CLK), .CLR(CLR), .OUT(ram_1x8_1_out), .INPUT(INPUT));
  RAM_1X8 ram_1x8_2 (.ADDR(demultiplexer_1_out1), .CLK(R_W), .R_W(CLK), .CLR(CLR), .OUT(ram_1x8_2_out), .INPUT(INPUT));
  RAM_1X8 ram_1x8_3 (.ADDR(demultiplexer_1_out2), .CLK(R_W), .R_W(CLK), .CLR(CLR), .OUT(ram_1x8_3_out), .INPUT(INPUT));
  RAM_1X8 ram_1x8_4 (
    .ADDR(demultiplexer_1_out3), .CLK(R_W), .R_W(CLK), .OUT(ram_1x8_4_out), .INPUT(INPUT));  // open: CLR
  Multiplexer #(.select(2), .width(8)) multiplexer_1 (
    .in0(ram_1x8_1_out), .in1(ram_1x8_2_out), .in2(ram_1x8_3_out), .in3(ram_1x8_4_out), .out(OUT), .sel(ADDR));  // open: en
endmodule

// 1X8(2)
module RAM_1X8_2 (
  input  ADDR,
  input  CLK,
  input  R_W,
  input  [7:0] INPUT,
  input  CLR,
  output [7:0] OUT
);

  wire and_1_out, j_k_ff_1_q, j_k_ff_2_q, j_k_ff_3_q, j_k_ff_4_q, j_k_ff_5_q, j_k_ff_6_q, j_k_ff_7_q,
       j_k_ff_8_q, not_1_out, not_2_out, not_3_out, not_4_out, not_5_out, not_6_out, not_7_out, not_8_out;

  and and_1 (and_1_out, CLK, R_W, ADDR);
  not not_1 (not_1_out, INPUT[0]);
  not not_2 (not_2_out, INPUT[1]);
  J_K_Flip_Flop j_k_ff_1 (
    .J(INPUT[0]), .clk(and_1_out), .K(not_1_out), .Q(j_k_ff_1_q), .reset(CLR));  // open: Qn, preset, en
  J_K_Flip_Flop j_k_ff_2 (
    .J(INPUT[1]), .clk(and_1_out), .K(not_2_out), .Q(j_k_ff_2_q), .reset(CLR));  // open: Qn, preset, en
  not not_3 (not_3_out, INPUT[2]);
  and and_2 (OUT[0], ADDR, j_k_ff_1_q);
  and and_3 (OUT[1], ADDR, j_k_ff_2_q);
  and and_4 (OUT[2], ADDR, j_k_ff_3_q);
  J_K_Flip_Flop j_k_ff_3 (
    .J(INPUT[2]), .clk(and_1_out), .K(not_3_out), .Q(j_k_ff_3_q), .reset(CLR));  // open: Qn, preset, en
  J_K_Flip_Flop j_k_ff_4 (
    .J(INPUT[3]), .clk(and_1_out), .K(not_4_out), .Q(j_k_ff_4_q), .reset(CLR));  // open: Qn, preset, en
  not not_4 (not_4_out, INPUT[3]);
  and and_5 (OUT[3], ADDR, j_k_ff_4_q);
  not not_5 (not_5_out, INPUT[4]);
  and and_6 (OUT[4], ADDR, j_k_ff_5_q);
  J_K_Flip_Flop j_k_ff_5 (
    .J(INPUT[4]), .clk(and_1_out), .K(not_5_out), .Q(j_k_ff_5_q), .reset(CLR));  // open: Qn, preset, en
  J_K_Flip_Flop j_k_ff_6 (
    .J(INPUT[5]), .clk(and_1_out), .K(not_6_out), .Q(j_k_ff_6_q), .reset(CLR));  // open: Qn, preset, en
  not not_6 (not_6_out, INPUT[5]);
  and and_7 (OUT[5], ADDR, j_k_ff_6_q);
  J_K_Flip_Flop j_k_ff_7 (
    .J(INPUT[6]), .clk(and_1_out), .K(not_7_out), .Q(j_k_ff_7_q), .reset(CLR));  // open: Qn, preset, en
  not not_7 (not_7_out, INPUT[6]);
  and and_8 (OUT[6], ADDR, j_k_ff_7_q);
  J_K_Flip_Flop j_k_ff_8 (
    .J(INPUT[7]), .clk(and_1_out), .K(not_8_out), .Q(j_k_ff_8_q), .reset(CLR));  // open: Qn, preset, en
  not not_8 (not_8_out, INPUT[7]);
  and and_9 (OUT[7], ADDR, j_k_ff_8_q);
endmodule

module RAM_8X8 (
  input  [2:0] ADDR,
  input  CLK,
  input  [7:0] INPUT,
  input  R_W,
  input  CLR,
  output [7:0] OUT
);

  wire demultiplexer_1_out0, demultiplexer_1_out1, demultiplexer_1_out2, demultiplexer_1_out3,
       demultiplexer_1_out4, demultiplexer_1_out5, demultiplexer_1_out6, demultiplexer_1_out7;
  wire [7:0] ram_1x8_2_1_out, ram_1x8_2_2_out, ram_1x8_2_3_out, ram_1x8_2_4_out, ram_1x8_2_5_out,
       ram_1x8_2_6_out, ram_1x8_2_7_out, ram_1x8_2_8_out;

  Demultiplexer #(.select(3)) demultiplexer_1 (
    .out0(demultiplexer_1_out0), .out1(demultiplexer_1_out1), .out2(demultiplexer_1_out2),
    .out3(demultiplexer_1_out3), .out4(demultiplexer_1_out4), .out5(demultiplexer_1_out5),
    .out6(demultiplexer_1_out6), .out7(demultiplexer_1_out7), .in(1'b1), .sel(ADDR));  // open: en
  RAM_1X8_2 ram_1x8_2_1 (
    .ADDR(demultiplexer_1_out0), .CLK(R_W), .R_W(CLK), .CLR(CLR), .OUT(ram_1x8_2_1_out), .INPUT(INPUT));
  RAM_1X8_2 ram_1x8_2_2 (
    .ADDR(demultiplexer_1_out1), .CLK(R_W), .R_W(CLK), .CLR(CLR), .OUT(ram_1x8_2_2_out), .INPUT(INPUT));
  RAM_1X8_2 ram_1x8_2_3 (
    .ADDR(demultiplexer_1_out2), .CLK(R_W), .R_W(CLK), .CLR(CLR), .OUT(ram_1x8_2_3_out), .INPUT(INPUT));
  RAM_1X8_2 ram_1x8_2_4 (
    .ADDR(demultiplexer_1_out3), .CLK(R_W), .R_W(CLK), .CLR(CLR), .OUT(ram_1x8_2_4_out), .INPUT(INPUT));
  RAM_1X8_2 ram_1x8_2_5 (
    .ADDR(demultiplexer_1_out4), .CLK(R_W), .R_W(CLK), .CLR(CLR), .OUT(ram_1x8_2_5_out), .INPUT(INPUT));
  RAM_1X8_2 ram_1x8_2_6 (
    .ADDR(demultiplexer_1_out5), .CLK(R_W), .R_W(CLK), .CLR(CLR), .OUT(ram_1x8_2_6_out), .INPUT(INPUT));
  RAM_1X8_2 ram_1x8_2_7 (
    .ADDR(demultiplexer_1_out6), .CLK(R_W), .R_W(CLK), .CLR(CLR), .OUT(ram_1x8_2_7_out), .INPUT(INPUT));
  RAM_1X8_2 ram_1x8_2_8 (
    .ADDR(demultiplexer_1_out7), .CLK(R_W), .R_W(CLK), .CLR(CLR), .OUT(ram_1x8_2_8_out), .INPUT(INPUT));
  Multiplexer #(.select(3), .width(8)) multiplexer_1 (
    .in0(ram_1x8_2_1_out), .in1(ram_1x8_2_2_out), .in2(ram_1x8_2_3_out), .in3(ram_1x8_2_4_out),
    .in4(ram_1x8_2_5_out), .in5(ram_1x8_2_6_out), .in6(ram_1x8_2_7_out), .in7(ram_1x8_2_8_out), .out(OUT),
    .sel(ADDR));  // open: en
endmodule
