// Logisim project exercicio01.circ as structural Verilog: 1 circuit, main circuit main
module main (
  input  addr,
  input  r_w,
  input  clk,
  input  IN,
  input  CLR,
  output out
);

  wire and_1_out, j_k_ff_1_q;

  and and_1 (and_1_out, addr, r_w, clk);
  J_K_Flip_Flop j_k_ff_1 (.J(and_1_out), .K(IN), .Q(j_k_ff_1_q), .reset(CLR));  // open: clk, Qn, preset, en
  J_K_Flip_Flop j_k_ff_2 (.J(and_1_out), .K(IN), .Q(j_k_ff_1_q));  // open: clk, Qn, preset, en, reset
  J_K_Flip_Flop j_k_ff_3 (.J(and_1_out), .K(IN), .Q(j_k_ff_1_q));  // open: clk, Qn, preset, en, reset
  J_K_Flip_Flop j_k_ff_4 (.J(and_1_out), .K(IN), .Q(j_k_ff_1_q));  // open: clk, Qn, preset, en, reset
  and and_2 (out, j_k_ff_1_q, addr);

  // Notes on the sheet:
  //   LUIZ MARQUES DE OLIVEIRA-417138
endmodule
