// Logisim project exercicio04.circ as structural Verilog: 1 circuit, main circuit main
module main (
  input  ADDR,
  input  R_W,
  input  CLK,
  input  IN,
  output out_5
);

  wire and_1_out, j_k_ff_1_q;

  and and_1 (and_1_out, ADDR, R_W, CLK);
  J_K_Flip_Flop j_k_ff_1 (.J(and_1_out), .K(IN), .Q(j_k_ff_1_q));  // open: clk, Qn, preset, en, reset
  J_K_Flip_Flop j_k_ff_2 (.J(and_1_out), .K(IN), .Q(j_k_ff_1_q));  // open: clk, Qn, preset, en, reset
  J_K_Flip_Flop j_k_ff_3 (.J(and_1_out), .K(IN), .Q(j_k_ff_1_q));  // open: clk, Qn, preset, en, reset
  J_K_Flip_Flop j_k_ff_4 (.J(and_1_out), .K(IN), .Q(j_k_ff_1_q));  // open: clk, Qn, preset, en, reset
  J_K_Flip_Flop j_k_ff_5 (.J(and_1_out), .K(IN), .Q(j_k_ff_1_q));  // open: clk, Qn, preset, en, reset
  J_K_Flip_Flop j_k_ff_6 (.J(and_1_out), .K(IN), .Q(j_k_ff_1_q));  // open: clk, Qn, preset, en, reset
  J_K_Flip_Flop j_k_ff_7 (.J(and_1_out), .K(IN), .Q(j_k_ff_1_q));  // open: clk, Qn, preset, en, reset
  J_K_Flip_Flop j_k_ff_8 (.J(and_1_out), .K(IN), .Q(j_k_ff_1_q));  // open: clk, Qn, preset, en, reset
  and and_2 (out_5, j_k_ff_1_q, ADDR);

  // Notes on the sheet:
  //   LUIZ MARQUES DE OLIVEIRA - 417138
endmodule
