// Logisim project DmxMUx.circ as structural Verilog: 3 circuits, main circuit main
module main (
  input  in_1,
  input  [1:0] in_2,
  output out_3,
  output out_4,
  output out_5,
  output out_6
);

  wire not_1_out, not_2_out;

  not not_1 (not_1_out, in_2[0]);
  not not_2 (not_2_out, in_2[1]);
  and and_1 (out_3, in_1, not_1_out, not_2_out);
  and and_2 (out_4, in_1, in_2[0], not_2_out);
  and and_3 (out_5, in_1, in_2[1], not_1_out);
  and and_4 (out_6, in_1, in_2[1], in_2[0]);
endmodule

module DMX (
  input  in_1,
  input  [1:0] in_2,
  output out_3,
  output out_4,
  output out_5,
  output out_6
);

  wire not_1_out, not_2_out;

  not not_1 (not_1_out, in_2[0]);
  not not_2 (not_2_out, in_2[1]);
  and and_1 (out_3, in_1, not_1_out, not_2_out);
  and and_2 (out_4, in_1, in_2[0], not_2_out);
  and and_3 (out_5, in_1, in_2[1], not_1_out);
  and and_4 (out_6, in_1, in_2[1], in_2[0]);
endmodule

module MUX (
  input  [7:0] in_1,
  input  [7:0] in_2,
  input  [7:0] in_3,
  input  [7:0] in_4,
  input  [1:0] in_5,
  output [7:0] out_6
);

  wire and_1_out, and_2_out, and_3_out, and_4_out, not_1_out, not_2_out;
  wire [7:0] controlled_buffer_1_out, controlled_buffer_2_out, controlled_buffer_3_out,
       controlled_buffer_4_out;

  not not_1 (not_1_out, in_5[0]);
  not not_2 (not_2_out, in_5[1]);
  assign controlled_buffer_1_out = and_1_out ? in_1 : 8'bz;  // Controlled_Buffer controlled_buffer_1
  and and_1 (and_1_out, not_2_out, not_1_out);
  assign controlled_buffer_2_out = and_2_out ? in_2 : 8'bz;  // Controlled_Buffer controlled_buffer_2
  and and_2 (and_2_out, in_5[0], not_2_out);
  assign controlled_buffer_3_out = and_3_out ? in_3 : 8'bz;  // Controlled_Buffer controlled_buffer_3
  and and_3 (and_3_out, in_5[1], not_1_out);
  assign controlled_buffer_4_out = and_4_out ? in_4 : 8'bz;  // Controlled_Buffer controlled_buffer_4
  and and_4 (and_4_out, in_5[1], in_5[0]);
  assign out_6 = controlled_buffer_1_out | controlled_buffer_2_out | controlled_buffer_3_out | controlled_buffer_4_out;  // OR_Gate or_1, 8 bits wide
endmodule
