// Logisim project Exercicio02.circ as structural Verilog: 3 circuits, main circuit main
module main (
  input  Addr,
  input  R_w,
  input  CLK,
  input  [7:0] Int,
  input  clean,
  output [7:0] out_6
);

  _1x4 u_1x4_1 (.ADDR(Addr), .R_W(R_w), .CLK(CLK), .Int(Int[3:0]), .clean(clean), .out_6(out_6[3:0]));
  _1x4 u_1x4_2 (.ADDR(Addr), .R_W(R_w), .CLK(CLK), .Int(Int[7:4]), .clean(clean), .out_6(out_6[7:4]));
endmodule

// 1x1
module Armazenador_1 (
  input  Addr,
  input  R_W,
  input  CLK,
  input  In,
  input  in_5,
  output Out
);

  wire and_1_out, j_k_ff_1_q, not_1_out;

  and and_1 (and_1_out, Addr, R_W, CLK);
  not not_1 (not_1_out, In);
  J_K_Flip_Flop j_k_ff_1 (
    .J(In), .clk(and_1_out), .K(not_1_out), .Q(j_k_ff_1_q), .reset(in_5));  // open: Qn, preset, en
  and and_2 (Out, Addr, j_k_ff_1_q);
endmodule

module _1x4 (
  input  ADDR,
  input  R_W,
  input  CLK,
  input  [3:0] Int,
  input  clean,
  output [3:0] out_6
);

  Armazenador_1 armazenador_1_1 (.Addr(ADDR), .R_W(R_W), .CLK(CLK), .In(Int[0]), .in_5(clean), .Out(out_6[0]));
  Armazenador_1 armazenador_1_2 (.Addr(ADDR), .R_W(R_W), .CLK(CLK), .In(Int[1]), .in_5(clean), .Out(out_6[1]));
  Armazenador_1 armazenador_1_3 (.Addr(ADDR), .R_W(R_W), .CLK(CLK), .In(Int[2]), .in_5(clean), .Out(out_6[2]));
  Armazenador_1 armazenador_1_4 (.Addr(ADDR), .R_W(R_W), .CLK(CLK), .In(Int[3]), .in_5(clean), .Out(out_6[3]));
endmodule
