// Logisim project Exercicio03.circ as structural Verilog: 4 circuits, main circuit main
module main (
  input  [1:0] ADDR,
  input  R_W,
  input  clock,
  input  [7:0] in_4,
  input  in_5,
  output [7:0] out_6
);

  wire demultiplexer_1_out0, demultiplexer_1_out1, demultiplexer_1_out2, demultiplexer_1_out3;
  wire [7:0] n1x8_1_out_6, n1x8_2_out_6, n1x8_3_out_6, n1x8_4_out_6;

  Demultiplexer #(.select(2)) demultiplexer_1 (
    .out0(demultiplexer_1_out0), .out1(demultiplexer_1_out1), .out2(demultiplexer_1_out2),
    .out3(demultiplexer_1_out3), .in(1'b1), .sel(ADDR));  // open: en
  _1x8 u_1x8_1 (.Addr(demultiplexer_1_out0), .R_w(R_W), .CLK(clock), .Int(in_4), .clean(in_5), .out_6(n1x8_1_out_6));
  _1x8 u_1x8_2 (.Addr(demultiplexer_1_out1), .R_w(R_W), .CLK(clock), .Int(in_4), .clean(in_5), .out_6(n1x8_2_out_6));
  _1x8 u_1x8_3 (.Addr(demultiplexer_1_out2), .R_w(R_W), .CLK(clock), .Int(in_4), .clean(in_5), .out_6(n1x8_3_out_6));
  _1x8 u_1x8_4 (.Addr(demultiplexer_1_out3), .R_w(R_W), .CLK(clock), .Int(in_4), .clean(in_5), .out_6(n1x8_4_out_6));
  Multiplexer #(.select(2), .width(8)) multiplexer_1 (
    .in0(n1x8_1_out_6), .in1(n1x8_2_out_6), .in2(n1x8_3_out_6), .in3(n1x8_4_out_6), .out(out_6), .sel(ADDR));  // open: en
endmodule

// 1x1
module Armazenador_1 (
  input  Addr,
  input  R_W,
  input  CLK,
  input  In,
  input  in_5,
  output Out
);

  wire and_1_out, j_k_ff_1_q, not_1_out;

  and and_1 (and_1_out, Addr, R_W, CLK);
  not not_1 (not_1_out, In);
  J_K_Flip_Flop j_k_ff_1 (
    .J(In), .clk(and_1_out), .K(not_1_out), .Q(j_k_ff_1_q), .reset(in_5));  // open: Qn, preset, en
  and and_2 (Out, Addr, j_k_ff_1_q);
endmodule

module _1x4 (
  input  ADDR,
  input  R_W,
  input  CLK,
  input  [3:0] Int,
  input  clean,
  output [3:0] out_6
);

  Armazenador_1 armazenador_1_1 (.Addr(ADDR), .R_W(R_W), .CLK(CLK), .In(Int[0]), .in_5(clean), .Out(out_6[0]));
  Armazenador_1 armazenador_1_2 (.Addr(ADDR), .R_W(R_W), .CLK(CLK), .In(Int[1]), .in_5(clean), .Out(out_6[1]));
  Armazenador_1 armazenador_1_3 (.Addr(ADDR), .R_W(R_W), .CLK(CLK), .In(Int[2]), .in_5(clean), .Out(out_6[2]));
  Armazenador_1 armazenador_1_4 (.Addr(ADDR), .R_W(R_W), .CLK(CLK), .In(Int[3]), .in_5(clean), .Out(out_6[3]));
endmodule

module _1x8 (
  input  Addr,
  input  R_w,
  input  CLK,
  input  [7:0] Int,
  input  clean,
  output [7:0] out_6
);

  _1x4 u_1x4_1 (.ADDR(Addr), .R_W(R_w), .CLK(CLK), .Int(Int[3:0]), .clean(clean), .out_6(out_6[3:0]));
  _1x4 u_1x4_2 (.ADDR(Addr), .R_W(R_w), .CLK(CLK), .Int(Int[7:4]), .clean(clean), .out_6(out_6[7:4]));
endmodule
