// Logisim project Exercicio05.circ as structural Verilog: 3 circuits, main circuit main
module main (
  input  [2:0] Addr,
  input  r_w,
  input  clk,
  input  [7:0] \int ,
  input  clean,
  output [7:0] out_6,
  output [7:0] out_7
);

  wire demultiplexer_1_out0, demultiplexer_1_out1, demultiplexer_1_out2, demultiplexer_1_out3,
       demultiplexer_1_out4, demultiplexer_1_out5, demultiplexer_1_out6, demultiplexer_1_out7;
  wire [7:0] n1x8_2_out_6, n1x8_3_out_6, n1x8_4_out_6, n1x8_5_out_6, n1x8_6_out_6, n1x8_7_out_6, n1x8_8_out_6;

  Demultiplexer #(.select(3)) demultiplexer_1 (
    .out0(demultiplexer_1_out0), .out1(demultiplexer_1_out1), .out2(demultiplexer_1_out2),
    .out3(demultiplexer_1_out3), .out4(demultiplexer_1_out4), .out5(demultiplexer_1_out5),
    .out6(demultiplexer_1_out6), .out7(demultiplexer_1_out7), .in(1'b1), .sel(Addr));  // open: en
  _1x8 u_1x8_1 (.ADDR(demultiplexer_1_out0), .R_W(r_w), .CLK(clk), .out_6(out_6), .Int(\int ), .clean(clean));
  _1x8 u_1x8_2 (.ADDR(demultiplexer_1_out1), .R_W(r_w), .CLK(clk), .out_6(n1x8_2_out_6), .Int(\int ), .clean(clean));
  _1x8 u_1x8_3 (.ADDR(demultiplexer_1_out2), .R_W(r_w), .CLK(clk), .out_6(n1x8_3_out_6), .Int(\int ), .clean(clean));
  _1x8 u_1x8_4 (.ADDR(demultiplexer_1_out3), .R_W(r_w), .CLK(clk), .out_6(n1x8_4_out_6), .Int(\int ), .clean(clean));
  _1x8 u_1x8_5 (.ADDR(demultiplexer_1_out4), .R_W(r_w), .CLK(clk), .out_6(n1x8_5_out_6), .Int(\int ), .clean(clean));
  _1x8 u_1x8_6 (.ADDR(demultiplexer_1_out5), .R_W(r_w), .CLK(clk), .out_6(n1x8_6_out_6), .Int(\int ), .clean(clean));
  _1x8 u_1x8_7 (.ADDR(demultiplexer_1_out6), .R_W(r_w), .CLK(clk), .out_6(n1x8_7_out_6), .Int(\int ), .clean(clean));
  _1x8 u_1x8_8 (.ADDR(demultiplexer_1_out7), .R_W(r_w), .CLK(clk), .out_6(n1x8_8_out_6), .Int(\int ), .clean(clean));
  Multiplexer #(.select(3), .width(8)) multiplexer_1 (
    .in0(out_6), .in1(n1x8_2_out_6), .in2(n1x8_3_out_6), .in3(n1x8_4_out_6), .in4(n1x8_5_out_6),
    .in5(n1x8_6_out_6), .in6(n1x8_7_out_6), .in7(n1x8_8_out_6), .out(out_7), .sel(Addr));  // open: en
endmodule

// 1x1
module Armazenador_1 (
  input  Addr,
  input  R_W,
  input  CLK,
  input  In,
  input  in_5,
  output Out
);

  wire and_1_out, j_k_ff_1_q, not_1_out;

  and and_1 (and_1_out, Addr, R_W, CLK);
  not not_1 (not_1_out, In);
  J_K_Flip_Flop j_k_ff_1 (
    .J(In), .clk(and_1_out), .K(not_1_out), .Q(j_k_ff_1_q), .reset(in_5));  // open: Qn, preset, en
  and and_2 (Out, Addr, j_k_ff_1_q);
endmodule

module _1x8 (
  input  ADDR,
  input  R_W,
  input  CLK,
  input  [7:0] Int,
  input  clean,
  output [7:0] out_6
);

  Armazenador_1 armazenador_1_1 (.Addr(ADDR), .R_W(R_W), .CLK(CLK), .In(Int[0]), .in_5(clean), .Out(out_6[0]));
  Armazenador_1 armazenador_1_2 (.Addr(ADDR), .R_W(R_W), .CLK(CLK), .In(Int[1]), .in_5(clean), .Out(out_6[1]));
  Armazenador_1 armazenador_1_3 (.Addr(ADDR), .R_W(R_W), .CLK(CLK), .In(Int[2]), .in_5(clean), .Out(out_6[2]));
  Armazenador_1 armazenador_1_4 (.Addr(ADDR), .R_W(R_W), .CLK(CLK), .In(Int[3]), .in_5(clean), .Out(out_6[3]));
  Armazenador_1 armazenador_1_5 (.Addr(ADDR), .R_W(R_W), .CLK(CLK), .In(Int[4]), .in_5(clean), .Out(out_6[4]));
  Armazenador_1 armazenador_1_6 (.Addr(ADDR), .R_W(R_W), .CLK(CLK), .In(Int[5]), .in_5(clean), .Out(out_6[5]));
  Armazenador_1 armazenador_1_7 (.Addr(ADDR), .R_W(R_W), .CLK(CLK), .In(Int[6]), .in_5(clean), .Out(out_6[6]));
  Armazenador_1 armazenador_1_8 (.Addr(ADDR), .R_W(R_W), .CLK(CLK), .In(Int[7]), .in_5(clean), .Out(out_6[7]));
endmodule
