// Logisim project Exemplo0102.circ as structural Verilog: 4 circuits, main circuit Exemplo0102
module Exemplo0102 (
  input  ADD,
  input  R_W,
  input  CLK,
  input  [7:0] IN,
  input  CLR,
  output [7:0] OUT
);

  Memoria_1x8 memoria_1x8_1 (.ADD(ADD), .R_W(R_W), .CLK(CLK), .IN(IN), .CLR(CLR), .OUT(OUT));

  // Notes on the sheet:
  //   Mateus Augusto Moraes Ferreira    Matricula:435669
endmodule

// M 1x1
module Memoria_1x1 (
  input  ADD,
  input  R_W,
  input  CLK,
  input  CLR,
  input  IN,
  output OUT
);

  wire and1_out, j_k_ff_1_q;

  and and1 (and1_out, ADD, R_W, CLK);
  J_K_Flip_Flop j_k_ff_1 (.J(IN), .clk(and1_out), .K(IN), .Q(j_k_ff_1_q), .reset(CLR));  // open: Qn, preset, en
  and and2 (OUT, ADD, j_k_ff_1_q);

  // Notes on the sheet:
  //   Mateus Augusto Moraes Ferreira    Matricula:435669
  //   Memoria 1x1
endmodule

// M 1x4
module Memoria_1x4 (
  input  ADD,
  input  R_W,
  input  CLK,
  input  [3:0] IN,
  input  CLR,
  output [3:0] OUT
);

  Memoria_1x1 memoria_1x1_1 (.ADD(ADD), .R_W(R_W), .CLK(CLK), .IN(IN[0]), .CLR(CLR), .OUT(OUT[0]));
  Memoria_1x1 memoria_1x1_2 (.ADD(ADD), .R_W(R_W), .CLK(CLK), .IN(IN[1]), .CLR(CLR), .OUT(OUT[1]));
  Memoria_1x1 memoria_1x1_3 (.ADD(ADD), .R_W(R_W), .CLK(CLK), .IN(IN[2]), .CLR(CLR), .OUT(OUT[2]));
  Memoria_1x1 memoria_1x1_4 (.ADD(ADD), .R_W(R_W), .CLK(CLK), .IN(IN[3]), .CLR(CLR), .OUT(OUT[3]));

  // Notes on the sheet:
  //   Mateus Augusto Moraes Ferreira    Matricula:435669
  //   Memoria 1x4
endmodule

// M 1x8
module Memoria_1x8 (
  input  ADD,
  input  R_W,
  input  CLK,
  input  [7:0] IN,
  input  CLR,
  output [7:0] OUT
);

  Memoria_1x4 memoria_1x4_1 (.ADD(ADD), .R_W(R_W), .CLK(CLK), .IN(IN[3:0]), .CLR(CLR), .OUT(OUT[3:0]));
  Memoria_1x4 memoria_1x4_2 (.ADD(ADD), .R_W(R_W), .CLK(CLK), .IN(IN[7:4]), .CLR(CLR), .OUT(OUT[7:4]));

  // Notes on the sheet:
  //   Mateus Augusto Moraes Ferreira    Matricula:435669
  //   Memoria 1x8
endmodule
