// Logisim project Exemplo0105.circ as structural Verilog: 3 circuits, main circuit Exemplo0105
module Exemplo0105 (
  input  ADD,
  input  R_W,
  input  CLK,
  input  [31:0] in_4,
  input  [31:0] in_5,
  input  CLR,
  output [31:0] out_7,
  output [31:0] out_8
);

  Memoria_8x8_JK memoria_8x8_jk_1 (
    .ADD(ADD), .R_W(R_W), .CLK(CLK), .IN(in_4), .in_5(in_5), .CLR(CLR), .OUT(out_7), .out_8(out_8));

  // Notes on the sheet:
  //   IN
  //   Mateus Augusto Moraes Ferreira     Matricula: 435669
  //   OUT
endmodule

// 1x8 JK
module Memoria_1x8_JK (
  input  ADD,
  input  R_W,
  input  CLK,
  input  CLR,
  input  [7:0] IN,
  output [7:0] OUT
);

  wire and1_out, j_k_ff_1_q, j_k_ff_2_q, j_k_ff_3_q, j_k_ff_4_q, j_k_ff_5_q, j_k_ff_6_q, j_k_ff_7_q,
       j_k_ff_8_q;

  and and1 (and1_out, ADD, R_W, CLK);
  and and2 (OUT[0], ADD, j_k_ff_1_q);
  J_K_Flip_Flop j_k_ff_1 (.J(IN[0]), .clk(and1_out), .K(IN[0]), .Q(j_k_ff_1_q), .reset(CLR));  // open: Qn, preset, en
  and and3 (OUT[1], ADD, j_k_ff_2_q);
  J_K_Flip_Flop j_k_ff_2 (.J(IN[1]), .clk(and1_out), .K(IN[1]), .Q(j_k_ff_2_q), .reset(CLR));  // open: Qn, preset, en
  and and4 (OUT[2], ADD, j_k_ff_3_q);
  J_K_Flip_Flop j_k_ff_3 (.J(IN[2]), .clk(and1_out), .K(IN[2]), .Q(j_k_ff_3_q), .reset(CLR));  // open: Qn, preset, en
  and and5 (OUT[3], ADD, j_k_ff_4_q);
  J_K_Flip_Flop j_k_ff_4 (.J(IN[3]), .clk(and1_out), .K(IN[3]), .Q(j_k_ff_4_q), .reset(CLR));  // open: Qn, preset, en
  and and6 (OUT[4], ADD, j_k_ff_5_q);
  J_K_Flip_Flop j_k_ff_5 (.J(IN[4]), .clk(and1_out), .K(IN[4]), .Q(j_k_ff_5_q), .reset(CLR));  // open: Qn, preset, en
  and and7 (OUT[5], ADD, j_k_ff_6_q);
  J_K_Flip_Flop j_k_ff_6 (.J(IN[5]), .clk(and1_out), .K(IN[5]), .Q(j_k_ff_6_q), .reset(CLR));  // open: Qn, preset, en
  and and8 (OUT[6], ADD, j_k_ff_7_q);
  J_K_Flip_Flop j_k_ff_7 (.J(IN[6]), .clk(and1_out), .K(IN[6]), .Q(j_k_ff_7_q), .reset(CLR));  // open: Qn, preset, en
  and and9 (OUT[7], ADD, j_k_ff_8_q);
  J_K_Flip_Flop j_k_ff_8 (.J(IN[7]), .clk(and1_out), .K(IN[7]), .Q(j_k_ff_8_q), .reset(CLR));  // open: Qn, preset, en

  // Notes on the sheet:
  //   Mateus Augusto Moraes Ferreira     Matricula: 435669
  //   Memoria 1x8 Flip Floop JK
endmodule

// M 8x8 JK
module Memoria_8x8_JK (
  input  ADD,
  input  R_W,
  input  CLK,
  input  [31:0] IN,
  input  [31:0] in_5,
  input  CLR,
  output [31:0] OUT,
  output [31:0] out_8
);

  Memoria_1x8_JK memoria_1x8_jk_1 (.ADD(ADD), .R_W(R_W), .CLK(CLK), .IN(IN[7:0]), .CLR(CLR), .OUT(OUT[7:0]));
  Memoria_1x8_JK memoria_1x8_jk_2 (.ADD(ADD), .R_W(R_W), .CLK(CLK), .IN(IN[15:8]), .CLR(CLR), .OUT(OUT[15:8]));
  Memoria_1x8_JK memoria_1x8_jk_3 (.ADD(ADD), .R_W(R_W), .CLK(CLK), .IN(IN[23:16]), .CLR(CLR), .OUT(OUT[23:16]));
  Memoria_1x8_JK memoria_1x8_jk_4 (.ADD(ADD), .R_W(R_W), .CLK(CLK), .IN(IN[31:24]), .CLR(CLR), .OUT(OUT[31:24]));
  Memoria_1x8_JK memoria_1x8_jk_5 (.ADD(ADD), .R_W(R_W), .CLK(CLK), .IN(in_5[7:0]), .CLR(CLR), .OUT(out_8[7:0]));
  Memoria_1x8_JK memoria_1x8_jk_6 (.ADD(ADD), .R_W(R_W), .CLK(CLK), .IN(in_5[15:8]), .CLR(CLR), .OUT(out_8[15:8]));
  Memoria_1x8_JK memoria_1x8_jk_7 (.ADD(ADD), .R_W(R_W), .CLK(CLK), .IN(in_5[23:16]), .CLR(CLR), .OUT(out_8[23:16]));
  Memoria_1x8_JK memoria_1x8_jk_8 (.ADD(ADD), .R_W(R_W), .CLK(CLK), .IN(in_5[31:24]), .CLR(CLR), .OUT(out_8[31:24]));

  // Notes on the sheet:
  //   Mateus Augusto Moraes Ferreira     Matricula: 435669
  //   Memoria 8x8 JK
endmodule
