// Logisim project Guia 10 - circuito.circ as structural Verilog: 5 circuits, main circuit memoriaRAM1X4
module memoriaRAM1X4 (
  input  CLR,
  input  A,
  input  R_W,
  input  CLK,
  input  [3:0] \input ,
  output [3:0] out_6
);

  wire and_1_out, j_k_ff_1_q, j_k_ff_2_q, j_k_ff_3_q, j_k_ff_4_q, not_1_out, not_2_out, not_3_out, not_4_out;

  and and_1 (and_1_out, A, R_W, CLK);
  not not_1 (not_1_out, \input [0]);
  not not_2 (not_2_out, \input [1]);
  not not_3 (not_3_out, \input [2]);
  not not_4 (not_4_out, \input [3]);
  J_K_Flip_Flop j_k_ff_1 (
    .J(\input [0]), .clk(and_1_out), .K(not_1_out), .Q(j_k_ff_1_q), .reset(CLR));  // open: Qn, preset, en
  J_K_Flip_Flop j_k_ff_2 (
    .J(\input [1]), .clk(and_1_out), .K(not_2_out), .Q(j_k_ff_2_q), .reset(CLR));  // open: Qn, preset, en
  J_K_Flip_Flop j_k_ff_3 (
    .J(\input [2]), .clk(and_1_out), .K(not_3_out), .Q(j_k_ff_3_q), .reset(CLR));  // open: Qn, preset, en
  J_K_Flip_Flop j_k_ff_4 (
    .J(\input [3]), .clk(and_1_out), .K(not_4_out), .Q(j_k_ff_4_q), .reset(CLR));  // open: Qn, preset, en
  and and_2 (out_6[0], j_k_ff_1_q, A);
  and and_3 (out_6[1], j_k_ff_2_q, A);
  and and_4 (out_6[2], j_k_ff_3_q, A);
  and and_5 (out_6[3], j_k_ff_4_q, A);
endmodule

module memoriaRAM1X8 (
  input  A,
  input  R_W,
  input  CLEAR,
  input  [7:0] INPUT,
  output [7:0] out_5
);

  wire CLK_out;

  Clock CLK (.out(CLK_out));
  memoriaRAM1X4 memoriaram1x4_1 (
    .CLR(CLEAR), .A(A), .R_W(R_W), .CLK(CLK_out), .\input (INPUT[3:0]), .out_6(out_5[3:0]));
  memoriaRAM1X4 memoriaram1x4_2 (
    .CLR(CLEAR), .A(A), .R_W(R_W), .CLK(CLK_out), .\input (INPUT[7:4]), .out_6(out_5[7:4]));
endmodule

module memoriaRAM4X8 (
  input  CLEAR,
  input  A,
  input  R_W,
  input  CLK,
  input  [7:0] in_5,
  output [7:0] out_6
);

  wire and_1_out, j_k_ff_1_q, j_k_ff_2_q, j_k_ff_3_q, j_k_ff_4_q, j_k_ff_5_q, j_k_ff_6_q, j_k_ff_7_q,
       j_k_ff_8_q, not_1_out, not_2_out, not_3_out, not_4_out, not_5_out, not_6_out, not_7_out, not_8_out;

  and and_1 (and_1_out, A, R_W, CLK);
  J_K_Flip_Flop j_k_ff_1 (
    .J(in_5[0]), .clk(and_1_out), .K(not_1_out), .Q(j_k_ff_1_q), .reset(CLEAR));  // open: Qn, preset, en
  not not_1 (not_1_out, in_5[0]);
  J_K_Flip_Flop j_k_ff_2 (
    .J(in_5[1]), .clk(and_1_out), .K(not_2_out), .Q(j_k_ff_2_q), .reset(CLEAR));  // open: Qn, preset, en
  not not_2 (not_2_out, in_5[1]);
  J_K_Flip_Flop j_k_ff_3 (
    .J(in_5[2]), .clk(and_1_out), .K(not_3_out), .Q(j_k_ff_3_q), .reset(CLEAR));  // open: Qn, preset, en
  not not_3 (not_3_out, in_5[2]);
  J_K_Flip_Flop j_k_ff_4 (
    .J(in_5[3]), .clk(and_1_out), .K(not_4_out), .Q(j_k_ff_4_q), .reset(CLEAR));  // open: Qn, preset, en
  not not_4 (not_4_out, in_5[3]);
  J_K_Flip_Flop j_k_ff_5 (
    .J(in_5[4]), .clk(and_1_out), .K(not_5_out), .Q(j_k_ff_5_q), .reset(CLEAR));  // open: Qn, preset, en
  not not_5 (not_5_out, in_5[4]);
  J_K_Flip_Flop j_k_ff_6 (
    .J(in_5[5]), .clk(and_1_out), .K(not_6_out), .Q(j_k_ff_6_q), .reset(CLEAR));  // open: Qn, preset, en
  not not_6 (not_6_out, in_5[5]);
  J_K_Flip_Flop j_k_ff_7 (
    .J(in_5[6]), .clk(and_1_out), .K(not_7_out), .Q(j_k_ff_7_q), .reset(CLEAR));  // open: Qn, preset, en
  not not_7 (not_7_out, in_5[6]);
  J_K_Flip_Flop j_k_ff_8 (
    .J(in_5[7]), .clk(and_1_out), .K(not_8_out), .Q(j_k_ff_8_q), .reset(CLEAR));  // open: Qn, preset, en
  not not_8 (not_8_out, in_5[7]);
  and and_2 (out_6[0], j_k_ff_1_q, A);
  and and_3 (out_6[1], j_k_ff_2_q, A);
  and and_4 (out_6[2], j_k_ff_3_q, A);
  and and_5 (out_6[3], j_k_ff_4_q, A);
  and and_6 (out_6[4], j_k_ff_5_q, A);
  and and_7 (out_6[5], j_k_ff_6_q, A);
  and and_8 (out_6[6], j_k_ff_7_q, A);
  and and_9 (out_6[7], j_k_ff_8_q, A);
endmodule

module memoriaRAM1X8__flip_flop (
  input  [1:0] a,
  input  clear,
  input  r_w,
  input  clk,
  input  [7:0] entrada,
  output [7:0] out_6
);

  wire demultiplexer_1_out0, demultiplexer_1_out1, demultiplexer_1_out2, demultiplexer_1_out3;
  wire [7:0] memoriaram4x8_1_out_6, memoriaram4x8_2_out_6, memoriaram4x8_3_out_6, memoriaram4x8_4_out_6;

  Demultiplexer #(.select(2)) demultiplexer_1 (
    .out0(demultiplexer_1_out0), .out1(demultiplexer_1_out1), .out2(demultiplexer_1_out2),
    .out3(demultiplexer_1_out3), .in(1'b1), .sel(a));  // open: en
  memoriaRAM4X8 memoriaram4x8_1 (
    .CLEAR(clear), .A(demultiplexer_1_out0), .R_W(r_w), .CLK(clk), .in_5(entrada),
    .out_6(memoriaram4x8_1_out_6));
  memoriaRAM4X8 memoriaram4x8_2 (
    .CLEAR(clear), .A(demultiplexer_1_out1), .R_W(r_w), .CLK(clk), .in_5(entrada),
    .out_6(memoriaram4x8_2_out_6));
  memoriaRAM4X8 memoriaram4x8_3 (
    .CLEAR(clear), .A(demultiplexer_1_out2), .R_W(r_w), .CLK(clk), .in_5(entrada),
    .out_6(memoriaram4x8_3_out_6));
  memoriaRAM4X8 memoriaram4x8_4 (
    .CLEAR(clear), .A(demultiplexer_1_out3), .R_W(r_w), .CLK(clk), .in_5(entrada),
    .out_6(memoriaram4x8_4_out_6));
  assign out_6 = memoriaram4x8_1_out_6 | memoriaram4x8_2_out_6 | memoriaram4x8_3_out_6 | memoriaram4x8_4_out_6;  // OR_Gate or_1, 8 bits wide
endmodule

module memoriaRAM8X8 (
  input  [2:0] in_1,
  input  clear,
  input  r_w,
  input  clk,
  input  [7:0] entrada,
  output [7:0] out_6
);

  wire demultiplexer_1_out0, demultiplexer_1_out1, demultiplexer_1_out2, demultiplexer_1_out3,
       demultiplexer_1_out4, demultiplexer_1_out5, demultiplexer_1_out6, demultiplexer_1_out7;
  wire [7:0] memoriaram4x8_1_out_6, memoriaram4x8_2_out_6, memoriaram4x8_3_out_6, memoriaram4x8_4_out_6,
       memoriaram4x8_5_out_6, memoriaram4x8_6_out_6, memoriaram4x8_7_out_6, memoriaram4x8_8_out_6;

  Demultiplexer #(.select(3)) demultiplexer_1 (
    .out0(demultiplexer_1_out0), .out1(demultiplexer_1_out1), .out2(demultiplexer_1_out2),
    .out3(demultiplexer_1_out3), .out4(demultiplexer_1_out4), .out5(demultiplexer_1_out5),
    .out6(demultiplexer_1_out6), .out7(demultiplexer_1_out7), .in(1'b1), .sel(in_1));  // open: en
  memoriaRAM4X8 memoriaram4x8_1 (
    .CLEAR(clear), .A(demultiplexer_1_out0), .R_W(r_w), .CLK(clk), .in_5(entrada),
    .out_6(memoriaram4x8_1_out_6));
  memoriaRAM4X8 memoriaram4x8_2 (
    .CLEAR(clear), .A(demultiplexer_1_out1), .R_W(r_w), .CLK(clk), .in_5(entrada),
    .out_6(memoriaram4x8_2_out_6));
  memoriaRAM4X8 memoriaram4x8_3 (
    .CLEAR(clear), .A(demultiplexer_1_out2), .R_W(r_w), .CLK(clk), .in_5(entrada),
    .out_6(memoriaram4x8_3_out_6));
  memoriaRAM4X8 memoriaram4x8_4 (
    .CLEAR(clear), .A(demultiplexer_1_out3), .R_W(r_w), .CLK(clk), .in_5(entrada),
    .out_6(memoriaram4x8_4_out_6));
  memoriaRAM4X8 memoriaram4x8_5 (
    .CLEAR(clear), .A(demultiplexer_1_out4), .R_W(r_w), .CLK(clk), .in_5(entrada),
    .out_6(memoriaram4x8_5_out_6));
  memoriaRAM4X8 memoriaram4x8_6 (
    .CLEAR(clear), .A(demultiplexer_1_out5), .R_W(r_w), .CLK(clk), .in_5(entrada),
    .out_6(memoriaram4x8_6_out_6));
  memoriaRAM4X8 memoriaram4x8_7 (
    .CLEAR(clear), .A(demultiplexer_1_out6), .R_W(r_w), .CLK(clk), .in_5(entrada),
    .out_6(memoriaram4x8_7_out_6));
  memoriaRAM4X8 memoriaram4x8_8 (
    .CLEAR(clear), .A(demultiplexer_1_out7), .R_W(r_w), .CLK(clk), .in_5(entrada),
    .out_6(memoriaram4x8_8_out_6));
  assign out_6 = memoriaram4x8_1_out_6 | memoriaram4x8_2_out_6 | memoriaram4x8_3_out_6 | memoriaram4x8_4_out_6 | memoriaram4x8_5_out_6 | memoriaram4x8_6_out_6 | memoriaram4x8_7_out_6 | memoriaram4x8_8_out_6;  // OR_Gate or_1, 8 bits wide
endmodule
