// Logisim project extraCir.circ as structural Verilog: 1 circuit, main circuit main
module main (
  input  in_1,
  input  CLR,
  input  ADDR,
  input  [7:0] dta,
  output [7:0] s
);

  wire clock_1_out, j_k_ff_2_q, j_k_ff_3_q, j_k_ff_4_q, j_k_ff_5_q, j_k_ff_6_q, j_k_ff_7_q, j_k_ff_8_q;

  Clock clock_1 (.out(clock_1_out));
  and and_1 (dta[1], in_1, clock_1_out);
  J_K_Flip_Flop j_k_ff_1 (.J(dta[1]), .K(dta[1]), .Q(ADDR), .reset(CLR));  // open: clk, Qn, preset, en
  J_K_Flip_Flop j_k_ff_2 (.J(dta[1]), .K(dta[1]), .Q(j_k_ff_2_q), .reset(CLR));  // open: clk, Qn, preset, en
  J_K_Flip_Flop j_k_ff_3 (.J(dta[2]), .clk(dta[1]), .K(dta[2]), .Q(j_k_ff_3_q), .reset(CLR));  // open: Qn, preset, en
  J_K_Flip_Flop j_k_ff_4 (.J(dta[3]), .clk(dta[1]), .K(dta[3]), .Q(j_k_ff_4_q), .reset(CLR));  // open: Qn, preset, en
  J_K_Flip_Flop j_k_ff_5 (.J(dta[4]), .clk(dta[1]), .K(dta[4]), .Q(j_k_ff_5_q), .reset(CLR));  // open: Qn, preset, en
  J_K_Flip_Flop j_k_ff_6 (.J(dta[5]), .clk(dta[1]), .K(dta[5]), .Q(j_k_ff_6_q), .reset(CLR));  // open: Qn, preset, en
  J_K_Flip_Flop j_k_ff_7 (.J(dta[6]), .clk(dta[1]), .K(dta[6]), .Q(j_k_ff_7_q), .reset(CLR));  // open: Qn, preset, en
  J_K_Flip_Flop j_k_ff_8 (.J(dta[7]), .clk(dta[1]), .K(dta[7]), .Q(j_k_ff_8_q), .reset(CLR));  // open: Qn, preset, en
  and and_2 (s[1], ADDR, ADDR);
  buf and_3 (s[1], j_k_ff_2_q);  // AND_Gate
  and and_4 (s[2], j_k_ff_3_q, ADDR);
  and and_5 (s[3], j_k_ff_4_q, ADDR);
  buf and_6 (s[4], j_k_ff_5_q);  // AND_Gate
  buf and_7 (s[5], ADDR);  // AND_Gate
  buf and_8 (s[6], j_k_ff_7_q);  // AND_Gate
  buf and_9 (s[7], ADDR);  // AND_Gate

  assign dta[0] = dta[1];
  assign s[0] = s[1];

  // Notes on the sheet:
  //   1x8
  //   Lorena Danielle Gonçalves Bento
endmodule
