// Logisim project Circuitos.circ as structural Verilog: 6 circuits, main circuit main
module main (
  input  [5:0] in_1,
  input  [5:0] in_2,
  input  in_3,
  input  [5:0] in_4,
  input  [5:0] in_5,
  input  in_6,
  input  [5:0] in_7,
  input  [5:0] in_8,
  input  in_9,
  input  [5:0] in_10,
  input  [5:0] in_11,
  output out_12,
  output out_13,
  output out_14,
  output out_15,
  output out_16,
  output out_17,
  output Overf,
  output out_19,
  output out_20,
  output Overf_2
);

  wire selecionador_1_s1, selecionador_2_s1, selecionador_3_s1, selecionador_4_s1, selecionador_6_s1;
  wire [5:0] ex01_1_out_4;

  Selecionador selecionador_1 (
    .in01(in_1[0]), .in02(in_2[0]), .C_in(in_3), .Selecionador(in_3), .s0(out_12), .s1(selecionador_1_s1));
  EX01 ex01_1 (
    .in_1(in_4), .in_2(in_7), .out_4(ex01_1_out_4[0]), .out_5(ex01_1_out_4[1]), .out_6(ex01_1_out_4[2]),
    .out_7(ex01_1_out_4[3]), .out_8(ex01_1_out_4[4]), .out_9(ex01_1_out_4[5]), .in_3(in_9), .Overf(Overf_2));
  Selecionador selecionador_2 (
    .in01(in_1[1]), .in02(in_2[1]), .C_in(selecionador_1_s1), .Selecionador(in_3), .s0(out_13),
    .s1(selecionador_2_s1));
  Selecionador selecionador_3 (
    .in01(in_1[2]), .in02(in_2[2]), .C_in(selecionador_2_s1), .Selecionador(in_3), .s0(out_14),
    .s1(selecionador_3_s1));
  Selecionador selecionador_4 (
    .in01(in_1[3]), .in02(in_2[3]), .C_in(selecionador_3_s1), .Selecionador(in_3), .s0(out_15),
    .s1(selecionador_4_s1));
  Selecionador selecionador_5 (
    .in01(in_1[4]), .in02(in_2[4]), .C_in(selecionador_4_s1), .Selecionador(in_3), .s0(out_16));  // open: s1
  Comparador comparador_1 (.in_1(ex01_1_out_4), .out_2(out_19));
  Selecionador selecionador_6 (
    .in01(in_1[5]), .in02(in_2[5]), .C_in(in_3), .Selecionador(in_3), .s0(out_17), .s1(selecionador_6_s1));
  xor xor_1 (Overf, in_3, selecionador_6_s1);
  EX01 ex01_2 (
    .in_1(in_8), .in_2(in_11), .out_4(in_5[5]), .out_5(in_5[4]), .out_6(in_5[3]), .out_7(in_5[2]),
    .out_8(in_5[1]), .out_9(in_5[4]), .in_3(in_6), .Overf(out_20));
  Cic1 cic1_1 (.in_1(in_6), .in_3(in_11), .in_4(in_10));  // open: in_2, out_5

  assign in_5[0] = in_5[4];

  // Notes on the sheet:
  //   EX01
  //   Ex02
  //   Ex03
endmodule

module Soma_Completa (
  input  C_in,
  input  in01,
  input  in02,
  output s0,
  output s1
);

  wire and_1_out, and_2_out, xor_1_out;

  xor xor_1 (xor_1_out, in01, in02);
  and and_1 (and_1_out, in01, in02);
  // XOR_Gate xor_2 has open pins: in0=C_in, in1=xor_1_out, out=open
  and and_2 (and_2_out, C_in, xor_1_out);
  or or_1 (s1, and_2_out, and_1_out);

  assign s0 = C_in;

  // Notes on the sheet:
  //   Soma Completa
endmodule

module Selecionador (
  input  in01,
  input  in02,
  input  C_in,
  input  Selecionador,
  output s0,
  output s1
);

  wire xor_1_out;

  xor xor_1 (xor_1_out, in02, Selecionador);
  Soma_Completa soma_completa_1 (.C_in(C_in), .in01(in01), .in02(xor_1_out), .s0(s0), .s1(s1));
endmodule

module EX01 (
  input  [5:0] in_1,
  input  [5:0] in_2,
  input  in_3,
  output out_4,
  output out_5,
  output out_6,
  output out_7,
  output out_8,
  output out_9,
  output Overf
);

  wire selecionador_1_s1, selecionador_2_s1, selecionador_3_s1, selecionador_4_s1, selecionador_6_s1;

  Selecionador selecionador_1 (
    .in01(in_1[0]), .in02(in_2[0]), .C_in(in_3), .Selecionador(in_3), .s0(out_4), .s1(selecionador_1_s1));
  Selecionador selecionador_2 (
    .in01(in_1[1]), .in02(in_2[1]), .C_in(selecionador_1_s1), .Selecionador(in_3), .s0(out_5),
    .s1(selecionador_2_s1));
  Selecionador selecionador_3 (
    .in01(in_1[2]), .in02(in_2[2]), .C_in(selecionador_2_s1), .Selecionador(in_3), .s0(out_6),
    .s1(selecionador_3_s1));
  Selecionador selecionador_4 (
    .in01(in_1[3]), .in02(in_2[3]), .C_in(selecionador_3_s1), .Selecionador(in_3), .s0(out_7),
    .s1(selecionador_4_s1));
  Selecionador selecionador_5 (
    .in01(in_1[4]), .in02(in_2[4]), .C_in(selecionador_4_s1), .Selecionador(in_3), .s0(out_8));  // open: s1
  Selecionador selecionador_6 (
    .in01(in_1[5]), .in02(in_2[5]), .C_in(in_3), .Selecionador(in_3), .s0(out_9), .s1(selecionador_6_s1));
  xor xor_1 (Overf, in_3, selecionador_6_s1);
endmodule

module Comparador (
  input  [5:0] in_1,
  output out_2
);

  wire not_1_out, not_2_out, not_3_out, not_4_out, not_5_out, not_6_out;

  not not_1 (not_1_out, in_1[0]);
  not not_2 (not_2_out, in_1[1]);
  not not_3 (not_3_out, in_1[2]);
  not not_4 (not_4_out, in_1[3]);
  not not_5 (not_5_out, in_1[4]);
  not not_6 (not_6_out, in_1[5]);
  and and_1 (out_2, not_1_out, not_2_out, not_3_out, not_4_out, not_5_out, not_6_out);
endmodule

module Cic1 (
  input  in_1,
  input  [5:0] in_2,
  input  [5:0] in_3,
  input  [5:0] in_4,
  output out_5
);

  EX01 ex01_1 (
    .in_1(in_4), .in_2(in_3), .out_4(in_2[5]), .out_5(in_2[4]), .out_6(in_2[3]), .out_7(in_2[2]),
    .out_8(in_2[1]), .out_9(in_2[0]), .in_3(in_1), .Overf(out_5));
endmodule
