// Logisim project Exercicio11.circ as structural Verilog: 1 circuit, main circuit main
module main (
  input  in_1,
  input  in_2,
  input  in_3,
  input  in_4,
  input  in_5,
  input  in_6,
  input  in_7,
  input  in_8,
  output out_9
);

  wire or_1_out;

  not not_1 (out_9, or_1_out);
  or or_1 (or_1_out, in_1, in_2, in_3, in_5, in_6, in_7, in_8);

  // Notes on the sheet:
  //   Lucas Siqueira Chagas - 380783
  //   TESTA SE TODOS OS BITS DE UM BYTE É IGUAL A 0
endmodule
