// Logisim project Extra011.circ as structural Verilog: 1 circuit, main circuit main
module main (
  input  A,
  input  B,
  input  C,
  input  D,
  input  E,
  input  F,
  input  G,
  input  H,
  output out_9
);

  wire and_1_out, or_1_out;

  and and_1 (and_1_out, A, B, C, D);
  or or_1 (or_1_out, E, F, G, H);
  nor nor_1 (out_9, and_1_out, or_1_out);

  // Notes on the sheet:
  //   S1
  //   S2
  //   João Henrique Mendes de Oliveira - 392734
  //   S
endmodule
