// Logisim project Guia0001_Extras.circ as structural Verilog: 1 circuit, main circuit main
module main (
  input  [7:0] in_1,
  input  [7:0] in_2,
  output [7:0] out_3,
  output [7:0] out_4
);

  wire [7:0] or_1_out;

  assign or_1_out = in_1 | in_2;  // OR_Gate or_1, 8 bits wide
  assign out_4 = in_2 & in_1;  // AND_Gate and_1, 8 bits wide
  assign out_3 = ~or_1_out;  // NOT_Gate not_1, 8 bits wide

  // Notes on the sheet:
  //   Nome:Fernando Silva
  //     Matricula:414506
endmodule
