// Logisim project ExercicioExtra1.circ as structural Verilog: 1 circuit, main circuit main
module main (
  input  [7:0] in_1,
  output out_2
);

  NotExactlyOne xnor_1 (
    .out(out_2), .in0(in_1[0]), .in1(in_1[1]), .in2(in_1[2]), .in3(in_1[3]), .in4(in_1[4]), .in5(in_1[5]),
    .in6(in_1[6]), .in7(in_1[7]));
endmodule
