// Logisim project ExercicioExtra1.circ as structural Verilog: 1 circuit, main circuit main
module main (
  input  [7:0] Entrada,
  output [7:0] \Saída 
);

  assign \Saída  = ~Entrada;  // NOT_Gate NOT, 8 bits wide
endmodule
