// Logisim project Extras0007.circ as structural Verilog: 2 circuits, main circuit main
module main (
  input  [7:0] in_1,
  output [7:0] \Saída 
);

  wire adder_1_cout;
  wire [7:0] complemento_de_1_1_out_2;

  Complemento_de_1 complemento_de_1_1 (.in_1(in_1), .out_2(complemento_de_1_1_out_2));
  // Probe on {8{1'b0}}
  Adder adder_1 (.a(complemento_de_1_1_out_2), .b({8{1'b0}}), .out(\Saída ), .cin(1'b1), .cout(adder_1_cout));
  // Probe on adder_1_cout

  // Notes on the sheet:
  //   Entrada = 1 byte ou 8 bits
  //   Complemento de 1
  //   João Henrique Mendes de Oliveira - 392734
  //   Complemento de 2
  //   + 1
endmodule

module Complemento_de_1 (
  input  [7:0] in_1,
  output [7:0] out_2
);

  assign out_2 = ~in_1;  // NOT_Gate not_1, 8 bits wide
endmodule
