// Logisim project Extras.circ as structural Verilog: 2 circuits, main circuit main
module main (
  input  [7:0] plus_1,
  input  [7:0] A,
  output [7:0] Complemento_de_1,
  output [7:0] Resultado_Complemento_de_2,
  output out_5
);

  wire [7:0] not_2_out;

  assign Complemento_de_1 = ~A;  // NOT_Gate not_1, 8 bits wide
  assign not_2_out = ~A;  // NOT_Gate not_2, 8 bits wide
  Adder adder_1 (.a(plus_1), .b(not_2_out), .out(Resultado_Complemento_de_2), .cout(out_5));  // open: cin
endmodule

module Soma (
  input  [7:0] in_1,
  input  [7:0] in_2,
  output [7:0] out_3,
  output [7:0] out_4
);

  assign out_3 = in_1 ^ in_2;  // XOR_Gate xor_1, 8 bits wide
  assign out_4 = in_1 & in_2;  // AND_Gate and_1, 8 bits wide
endmodule
