// Logisim project Extra0001.circ as structural Verilog: 1 circuit, main circuit main
module main (
  input  a,
  input  b,
  input  c,
  input  d,
  input  p,
  input  q,
  input  r,
  input  t,
  output s
);

  wire and_1_out, or_1_out;

  and and_1 (and_1_out, a, b, c, d);
  or or_1 (or_1_out, p, q, r, t);
  nor nor_1 (s, and_1_out, or_1_out);

  // Notes on the sheet:
  //   s1
  //   s2
endmodule
