// Logisim project Extra0002.circ as structural Verilog: 1 circuit, main circuit main
module main (
  input  a,
  input  b,
  input  c,
  input  d,
  input  p,
  input  q,
  input  r,
  input  t,
  output s
);

  wire or_1_out, or_2_out;

  or or_1 (or_1_out, a, b, c, d);
  or or_2 (or_2_out, p, q, r, t);
  or or_3 (s, or_1_out, or_2_out);

  // Notes on the sheet:
  //   s1
  //   s2
endmodule
