// Logisim project Extra1.circ as structural Verilog: 1 circuit, main circuit main
module main (
  input  [7:0] a,
  output [7:0] s
);

  assign s = ~a;  // NOT_Gate Complemento_de_1, 8 bits wide
endmodule
