// Logisim project extra2.circ as structural Verilog: 1 circuit, main circuit main
module main (
  input  in_1,
  input  in_2,
  input  in_3,
  input  in_4,
  input  in_5,
  input  in_6,
  input  in_7,
  input  in_8,
  input  in_9,
  output out_10,
  output out_11,
  output out_12,
  output out_13,
  output out_14,
  output out_15,
  output out_16,
  output out_17,
  output out_18,
  output out_19,
  output out_20,
  output out_21,
  output out_22,
  output out_23,
  output out_24,
  output out_25,
  output out_26
);

  wire and_1_out, and_2_out, and_3_out, and_4_out, and_5_out, and_6_out, and_7_out, and_8_out;

  not not_1 (out_11, in_1);
  not not_2 (out_13, in_2);
  not not_3 (out_15, in_3);
  not not_4 (out_17, in_4);
  not not_5 (out_19, in_5);
  not not_6 (out_21, in_6);
  not not_7 (out_23, in_7);
  not not_8 (out_26, in_8);
  not not_9 (out_12, and_1_out);
  and and_1 (and_1_out, out_11, and_2_out);
  not not_10 (out_14, and_2_out);
  and and_2 (and_2_out, out_13, and_3_out);
  not not_11 (out_16, and_3_out);
  and and_3 (and_3_out, out_15, and_4_out);
  and and_4 (and_4_out, out_17, and_5_out);
  not not_12 (out_18, and_4_out);
  and and_5 (and_5_out, out_19, and_6_out);
  not not_13 (out_20, and_5_out);
  not not_14 (out_22, and_6_out);
  and and_6 (and_6_out, out_21, and_7_out);
  and and_7 (and_7_out, out_23, out_25);
  not not_15 (out_24, and_7_out);
  and and_8 (and_8_out, out_26, in_9);
  not not_16 (out_25, and_8_out);

  // Notes on the sheet:
  //   lucas siqueira chagas - 380783
  //   extra02-01 -> complemento de 1
endmodule
