// Logisim project extra3.circ as structural Verilog: 1 circuit, main circuit main
module main (
  input  in_1,
  input  in_2,
  input  in_3,
  input  in_4,
  input  in_5,
  input  in_6,
  input  in_7,
  input  in_8,
  input  in_9,
  output out_10,
  output out_11,
  output out_12,
  output out_13,
  output out_14,
  output out_15,
  output out_16,
  output out_17,
  output out_18,
  output out_19,
  output out_20,
  output out_21,
  output out_22,
  output out_23,
  output out_24,
  output out_25,
  output out_26
);

  wire not_9_out, not_10_out, not_11_out, not_12_out, not_13_out, not_14_out, not_15_out, not_16_out;

  not not_1 (out_11, in_1);
  not not_2 (out_13, in_2);
  not not_3 (out_15, in_3);
  not not_4 (out_17, in_4);
  not not_5 (out_19, in_5);
  not not_6 (out_21, in_6);
  not not_7 (out_23, in_7);
  not not_8 (out_26, in_8);
  not not_9 (not_9_out, out_12);
  xor xor_1 (out_12, out_11, not_10_out);
  not not_10 (not_10_out, out_14);
  xor xor_2 (out_14, out_13, not_11_out);
  not not_11 (not_11_out, out_16);
  xor xor_3 (out_16, out_15, not_12_out);
  not not_12 (not_12_out, out_18);
  xor xor_4 (out_18, out_17, not_13_out);
  not not_13 (not_13_out, out_20);
  xor xor_5 (out_20, out_19, not_14_out);
  not not_14 (not_14_out, out_22);
  xor xor_6 (out_22, out_21, not_15_out);
  not not_15 (not_15_out, out_24);
  xor xor_7 (out_24, out_23, not_16_out);
  not not_16 (not_16_out, out_25);
  xor xor_8 (out_25, out_26, in_9);

  // Notes on the sheet:
  //   lucas siqueira chagas - 380783
  //   extra02-01 -> complemento de 1
endmodule
