// Logisim project extra4.circ as structural Verilog: 1 circuit, main circuit main
module main (
  input  in_1,
  input  in_2,
  input  in_3,
  input  in_4,
  input  in_5,
  output out_6,
  output out_7,
  output out_8,
  output out_9,
  output out_10,
  output out_11,
  output out_12,
  output out_13
);

  wire not_5_out, not_6_out;

  not not_1 (out_6, in_1);
  not not_2 (out_8, in_2);
  not not_3 (out_10, in_3);
  not not_4 (out_13, in_4);
  xor xor_1 (out_7, out_6, out_9);
  xor xor_2 (out_9, out_8, not_5_out);
  not not_5 (not_5_out, out_11);
  xor xor_3 (out_11, out_10, not_6_out);
  not not_6 (not_6_out, out_12);
  xor xor_4 (out_12, out_13, in_5);

  // Notes on the sheet:
  //   lucas siqueira chagas - 380783
  //   extra02-01 -> complemento de 1
endmodule
