// Logisim project extra5.circ as structural Verilog: 1 circuit, main circuit main
module main (
  input  in_1,
  input  in_2,
  input  in_3,
  input  in_4,
  input  in_5,
  input  in_6,
  output out_7,
  output out_8,
  output out_9,
  output out_10,
  output out_11,
  output out_12,
  output out_13,
  output out_14,
  output out_15,
  output out_16
);

  wire and_1_out, and_2_out, and_3_out, and_4_out;

  and and_1 (and_1_out, out_9, and_2_out);
  and and_2 (and_2_out, out_11, and_3_out);
  and and_3 (and_3_out, out_13, and_4_out);
  and and_4 (and_4_out, out_16, in_6);
  not not_1 (out_7, in_1);
  not not_2 (out_9, in_2);
  not not_3 (out_11, in_3);
  not not_4 (out_13, in_4);
  not not_5 (out_16, in_5);
  xor xor_1 (out_8, out_7, and_1_out);
  xor xor_2 (out_10, out_9, and_2_out);
  xor xor_3 (out_12, out_11, and_3_out);
  xor xor_4 (out_14, out_13, and_4_out);
  // NOT_Gate not_6 has open pins: in=out_15, out=open
  xor xor_5 (out_15, out_16, in_6);

  // Notes on the sheet:
  //   lucas siqueira chagas - 380783
  //   extra02-01 -> complemento de 1
endmodule
