// Logisim project Circuitos.circ as structural Verilog: 9 circuits, main circuit Exemplo0031
module Exemplo0031 (
  input  [3:0] a,
  input  [3:0] b,
  output [3:0] s,
  output [3:0] s2
);

  assign s = a & b;  // AND_Gate AND, 4 bits wide
  assign s2 = a | b;  // OR_Gate OR, 4 bits wide

  // Notes on the sheet:
  //   Exemplo0031 - Bruno Cezar Andrade  Viallet - 396679
endmodule

module Exemplo0032 (
  input  [1:0] a,
  input  [1:0] b,
  input  [1:0] Flag,
  output [1:0] s
);

  wire [1:0] AND_OR_s, AND_OR_s2, ANDA_out, ANDO_out;

  andor AND_OR (.a(a), .b(b), .s(AND_OR_s), .s2(AND_OR_s2));
  assign ANDO_out = AND_OR_s2 & ~Flag;  // AND_Gate ANDO, 2 bits wide
  assign ANDA_out = AND_OR_s & Flag;  // AND_Gate ANDA, 2 bits wide
  assign s = ANDA_out | ANDO_out;  // OR_Gate OR, 2 bits wide

  // Notes on the sheet:
  //   Exemplo0032 - Bruno Cezar Andrade  Viallet - 396679
  //   11 AND / 00 OR
endmodule

module Exemplo0033 (
  input  [1:0] a,
  input  [1:0] b,
  input  [1:0] Flag,
  output [1:0] s,
  output [1:0] z1
);

  wire [1:0] AND_OR_s, AND_OR_s2, ANDA_out, ANDNA_out, ANDNO_out, ANDO_out, NANDNOR_s, NANDNOR_s2;

  andor AND_OR (.a(a), .b(b), .s(AND_OR_s), .s2(AND_OR_s2));
  nandnor NANDNOR (.a(a), .b(b), .s(NANDNOR_s), .s2(NANDNOR_s2));
  assign ANDA_out = AND_OR_s & ~Flag;  // AND_Gate ANDA, 2 bits wide
  assign ANDO_out = AND_OR_s2 & ~Flag;  // AND_Gate ANDO, 2 bits wide
  assign ANDNA_out = NANDNOR_s & Flag;  // AND_Gate ANDNA, 2 bits wide
  assign ANDNO_out = NANDNOR_s2 & Flag;  // AND_Gate ANDNO, 2 bits wide
  assign s = ANDA_out | ANDNA_out;  // OR_Gate OR, 2 bits wide
  assign z1 = ANDO_out | ANDNO_out;  // OR_Gate OR2, 2 bits wide

  // Notes on the sheet:
  //   00 - AND/OR  ||| 11 - NAND/NOR
  //   Exemplo0033 - Bruno Cezar Andrade  Viallet - 396679
  //   AND / NAND
  //   OR / NOR
endmodule

module Exemplo0034 (
  input  [1:0] a,
  input  [1:0] b,
  input  [1:0] Flag,
  output [1:0] s,
  output [1:0] z1
);

  wire [1:0] ANDA_out, ANDNA_out, ANDNO_out, ANDO_out, ORNOR_s, ORNOR_s1, XORXNOR_s, XORXNOR_s1;

  XORXNOR XORXNOR (.a(a), .b(b), .s(XORXNOR_s), .s1(XORXNOR_s1));
  ORNOR ORNOR (.a(a), .b(b), .s(ORNOR_s), .s1(ORNOR_s1));
  assign ANDA_out = XORXNOR_s & ~Flag;  // AND_Gate ANDA, 2 bits wide
  assign ANDO_out = XORXNOR_s1 & ~Flag;  // AND_Gate ANDO, 2 bits wide
  assign ANDNA_out = ORNOR_s & Flag;  // AND_Gate ANDNA, 2 bits wide
  assign ANDNO_out = ORNOR_s1 & Flag;  // AND_Gate ANDNO, 2 bits wide
  assign s = ANDA_out | ANDNA_out;  // OR_Gate OR, 2 bits wide
  assign z1 = ANDO_out | ANDNO_out;  // OR_Gate OR2, 2 bits wide

  // Notes on the sheet:
  //   00 - XOR/XNOR  ||| 11 - OR/NOR
  //   Exemplo0034 - Bruno Cezar Andrade  Viallet - 396679
  //   XOR / OR
  //   XNOR / NOR
endmodule

module Exemplo0035 (
  input  in_1,
  input  in_2,
  output out_3,
  output out_4,
  output out_5,
  output out_6,
  output out_7,
  output out_8,
  output out_9
);

  not not_1 (out_3, in_2);
  or or_1 (out_4, in_1, in_2);
  nor nor_1 (out_5, in_1, in_2);
  and and_1 (out_6, in_1, in_2);
  nand nand_1 (out_7, in_1, in_2);
  xor xor_1 (out_8, in_1, in_2);
  xnor xnor_1 (out_9, in_1, in_2);

  // Notes on the sheet:
  //   Exemplo0035 - Bruno Cezar Andrade  Viallet - 396679
endmodule

module andor (
  input  [1:0] a,
  input  [1:0] b,
  output [1:0] s,
  output [1:0] s2
);

  assign s = a & b;  // AND_Gate AND, 2 bits wide
  assign s2 = a | b;  // OR_Gate OR, 2 bits wide

  // Notes on the sheet:
  //   AND/OR - Bruno Cezar Andrade  Viallet - 396679
endmodule

module nandnor (
  input  [1:0] a,
  input  [1:0] b,
  output [1:0] s,
  output [1:0] s2
);

  assign s = ~(a & b);  // NAND_Gate NAND, 2 bits wide
  assign s2 = ~(a | b);  // NOR_Gate NOR, 2 bits wide

  // Notes on the sheet:
  //   NAND/NOR - Bruno Cezar Andrade  Viallet - 396679
endmodule

module XORXNOR (
  input  [1:0] a,
  input  [1:0] b,
  output [1:0] s,
  output [1:0] s1
);

  assign s = a ^ b;  // XOR_Gate XOR, 2 bits wide
  assign s1 = ~(b ^ a);  // XNOR_Gate XNOR, 2 bits wide
endmodule

module ORNOR (
  input  [1:0] a,
  input  [1:0] b,
  output [1:0] s,
  output [1:0] s1
);

  assign s = a | b;  // OR_Gate OR, 2 bits wide
  assign s1 = ~(b | a);  // NOR_Gate NOR, 2 bits wide
endmodule
