// Logisim project Exemplo0031.circ as structural Verilog: 1 circuit, main circuit main
module main (
  input  [3:0] x,
  input  [3:0] y,
  output [3:0] s,
  output [3:0] s1
);

  assign s = y & x;  // AND_Gate AND, 4 bits wide
  assign s1 = y | x;  // OR_Gate OR, 4 bits wide

  // Notes on the sheet:
  //   Exemplo0031
endmodule
