// Logisim project Exemplo0033.circ as structural Verilog: 1 circuit, main circuit main
// 1
module main (
  input  [1:0] x,
  input  [1:0] y,
  input  [1:0] Flag,
  output [1:0] z1,
  output [1:0] z
);

  wire [1:0] and_2_out, and_3_out, and_4_out, and_5_out, AND_out, NAND_out, NOR_out, not_1_out, not_2_out,
       OR_out;

  assign AND_out = y & x;  // AND_Gate AND, 2 bits wide
  assign OR_out = x | y;  // OR_Gate OR, 2 bits wide
  assign NAND_out = ~(y & x);  // NAND_Gate NAND, 2 bits wide
  assign NOR_out = ~(x | y);  // NOR_Gate NOR, 2 bits wide
  assign not_1_out = ~Flag;  // NOT_Gate not_1, 2 bits wide
  assign not_2_out = ~Flag;  // NOT_Gate not_2, 2 bits wide
  assign and_2_out = AND_out & not_1_out;  // AND_Gate and_2, 2 bits wide
  assign and_3_out = OR_out & not_2_out;  // AND_Gate and_3, 2 bits wide
  assign and_4_out = NAND_out & Flag;  // AND_Gate and_4, 2 bits wide
  assign and_5_out = NOR_out & Flag;  // AND_Gate and_5, 2 bits wide
  assign z1 = and_5_out | and_3_out;  // OR_Gate or_2, 2 bits wide
  assign z = and_4_out | and_2_out;  // OR_Gate or_3, 2 bits wide
endmodule
