// Logisim project Exemplo0032_logisim.circ as structural Verilog: 2 circuits, main circuit main
module main (
  input  chave,
  input  a0,
  input  a1,
  input  b0,
  input  b1,
  output s0,
  output s1
);

  subcircuito subcircuito_1 (.chave(chave), .a0(a0), .a1(a1), .b0(b0), .b1(b1), .s1(s1), .s0(s0));
endmodule

module subcircuito (
  input  chave,
  input  a0,
  input  a1,
  input  b0,
  input  b1,
  output s1,
  output s0
);

  wire and_1_out, and_2_out, and_3_out, and_4_out, and_5_out, and_6_out, not_1_out, or_3_out, or_4_out;

  and and_1 (and_1_out, and_2_out, chave);
  and and_2 (and_2_out, a0, b0);
  and and_3 (and_3_out, a1, b1);
  and and_4 (and_4_out, and_3_out, chave);
  or or_1 (s1, and_4_out, and_5_out);
  or or_2 (s0, and_1_out, and_6_out);
  not not_1 (not_1_out, chave);
  or or_3 (or_3_out, a0, b0);
  or or_4 (or_4_out, a1, b1);
  and and_5 (and_5_out, or_4_out, not_1_out);
  and and_6 (and_6_out, or_3_out, not_1_out);
endmodule
