// Logisim project Exemplo0034_logisim.circ as structural Verilog: 4 circuits, main circuit main
module main (
  input  chave,
  input  a0,
  input  a1,
  input  b0,
  input  b1,
  output s2_0,
  output s2_1,
  output s1_0,
  output s1_1
);

  subcircuito subcircuito_1 (
    .chave(chave), .a0(a0), .a1(a1), .b0(b0), .b1(b1), .s2_0(s2_0), .s2_1(s2_1), .s1_0(s1_0), .s1_1(s1_1));  // open: s_or_nor_OR0, s_xor_xnor_XOR0, s_or_nor_OR1, s_xor_xnor_XOR1, s_or_nor_NOR0, s_xor_xnor_XNOR0, s_or_nor_NOR1, s_xor_xnor_XNOR1
endmodule

module or_nor (
  input  a0,
  input  a1,
  input  b0,
  input  b1,
  output s_or0,
  output s_nor0,
  output s_or1,
  output s_nor1
);

  or or_1 (s_or0, a0, b0);
  or or_2 (s_or1, a1, b1);
  nor nor_1 (s_nor0, a0, b0);
  nor nor_2 (s_nor1, a1, b1);
endmodule

module xor_xnor (
  input  a0,
  input  a1,
  input  b0,
  input  b1,
  output s_xor0,
  output s_xnor0,
  output s_xor1,
  output s_xnor1
);

  xor xor_1 (s_xor0, a0, b0);
  xor xor_2 (s_xor1, a1, b1);
  xnor xnor_1 (s_xnor0, a0, b0);
  xnor xnor_2 (s_xnor1, a1, b1);
endmodule

module subcircuito (
  input  chave,
  input  a0,
  input  a1,
  input  b0,
  input  b1,
  output s2_0,
  output s2_1,
  output s_or_nor_OR0,
  output s_or_nor_NOR0,
  output s_xor_xnor_XOR0,
  output s_xor_xnor_XNOR0,
  output s_or_nor_OR1,
  output s_or_nor_NOR1,
  output s_xor_xnor_XOR1,
  output s_xor_xnor_XNOR1,
  output s1_0,
  output s1_1
);

  wire and_1_out, and_2_out, and_3_out, and_4_out, and_5_out, and_6_out, and_7_out, and_8_out, not_1_out;

  or_nor or_nor_1 (
    .s_or0(s_or_nor_OR0), .s_or1(s_or_nor_OR1), .a0(a0), .a1(a1), .b0(b0), .b1(b1), .s_nor0(s_or_nor_NOR0),
    .s_nor1(s_or_nor_NOR1));
  not not_1 (not_1_out, chave);
  and and_1 (and_1_out, s_or_nor_OR1, not_1_out);
  and and_2 (and_2_out, s_or_nor_OR0, not_1_out);
  or or_1 (s1_0, and_2_out, and_3_out);
  or or_2 (s1_1, and_1_out, and_4_out);
  and and_3 (and_3_out, chave, s_xor_xnor_XOR0);
  and and_4 (and_4_out, chave, s_xor_xnor_XOR1);
  xor_xnor xor_xnor_1 (
    .s_xor0(s_xor_xnor_XOR0), .s_xor1(s_xor_xnor_XOR1), .a0(a0), .a1(a1), .b0(b0), .b1(b1),
    .s_xnor0(s_xor_xnor_XNOR0), .s_xnor1(s_xor_xnor_XNOR1));
  and and_5 (and_5_out, not_1_out, s_or_nor_NOR0);
  or or_3 (s2_0, and_5_out, and_6_out);
  and and_6 (and_6_out, chave, s_xor_xnor_XNOR0);
  and and_7 (and_7_out, not_1_out, s_or_nor_NOR1);
  or or_4 (s2_1, and_7_out, and_8_out);
  and and_8 (and_8_out, chave, s_xor_xnor_XNOR1);
endmodule
