// Logisim project Exemplo0035_logisim.circ as structural Verilog: 2 circuits, main circuit main
module main (
  input  a,
  input  b,
  output s_not_a,
  output s_not_b,
  output s_or,
  output s_nor,
  output s_and,
  output s_nand,
  output s_xor,
  output s_xnor
);

  subcircuito subcircuito_1 (
    .a(a), .b(b), .s_not_a(s_not_a), .s_not_b(s_not_b), .s_or(s_or), .s_nor(s_nor), .s_and(s_and),
    .s_nand(s_nand), .s_xor(s_xor), .s_xnor(s_xnor));
endmodule

module subcircuito (
  input  a,
  input  b,
  output s_not_a,
  output s_not_b,
  output s_or,
  output s_nor,
  output s_and,
  output s_nand,
  output s_xor,
  output s_xnor
);

  not not_1 (s_not_a, a);
  not not_2 (s_not_b, b);
  or or_1 (s_or, a, b);
  nor nor_1 (s_nor, a, b);
  and and_1 (s_and, a, b);
  nand nand_1 (s_nand, a, b);
  xor xor_1 (s_xor, a, b);
  xnor xnor_1 (s_xnor, a, b);
endmodule
