// Logisim project Guia03.circ as structural Verilog: 5 circuits, main circuit Ex1
module Ex1 (
  input  [3:0] in_1,
  input  [3:0] in_2,
  output [3:0] out_3,
  output [3:0] out_4
);

  assign out_3 = in_1 & in_2;  // AND_Gate and_1, 4 bits wide
  assign out_4 = in_1 | in_2;  // OR_Gate or_1, 4 bits wide

  // Notes on the sheet:
  //   Miller - 449048
  //   Arquitetura de Computadores - Theldo
  //   Portas AND e OR simultaneas
endmodule

module Ex2 (
  input  [1:0] in_1,
  input  [1:0] in_2,
  input  in_3,
  output [1:0] out_4
);

  wire [1:0] and_1_out, and_2_out, and_3_out, not_1_out, not_2_out, or_1_out;

  assign not_1_out = ~{2{in_3}};  // NOT_Gate not_1, 2 bits wide
  assign or_1_out = in_1 | in_2;  // OR_Gate or_1, 2 bits wide
  assign and_1_out = in_1 & in_2;  // AND_Gate and_1, 2 bits wide
  assign and_2_out = or_1_out & not_1_out;  // AND_Gate and_2, 2 bits wide
  assign not_2_out = ~not_1_out;  // NOT_Gate not_2, 2 bits wide
  assign and_3_out = not_2_out & and_1_out;  // AND_Gate and_3, 2 bits wide
  assign out_4 = and_2_out | and_3_out;  // OR_Gate or_2, 2 bits wide

  // Notes on the sheet:
  //   Miller - 449048
  //   AND e OR selecionavel
  //   Arquitetura de Computadores
endmodule

module Ex3 (
  input  Selecionar_Grupo,
  input  [1:0] in_2,
  input  [1:0] in_3,
  output [1:0] out_4,
  output [1:0] out_5,
  output [1:0] out_6,
  output [1:0] out_7
);

  wire [1:0] and_3_out, nand_1_out, nor_1_out, not_1_out, or_1_out;

  assign nand_1_out = ~(in_2 & in_3);  // NAND_Gate nand_1, 2 bits wide
  assign nor_1_out = ~(in_2 | in_3);  // NOR_Gate nor_1, 2 bits wide
  assign not_1_out = ~{2{Selecionar_Grupo}};  // NOT_Gate not_1, 2 bits wide
  assign out_4 = nand_1_out & {2{Selecionar_Grupo}};  // AND_Gate and_1, 2 bits wide
  assign out_5 = {2{Selecionar_Grupo}} & nor_1_out;  // AND_Gate and_2, 2 bits wide
  assign and_3_out = in_2 & in_3;  // AND_Gate and_3, 2 bits wide
  assign or_1_out = in_2 | in_3;  // OR_Gate or_1, 2 bits wide
  assign out_6 = and_3_out & not_1_out;  // AND_Gate and_4, 2 bits wide
  assign out_7 = not_1_out & or_1_out;  // AND_Gate and_5, 2 bits wide

  // Notes on the sheet:
  //   Valores de Entrada
  //   0 = AND/OR
  //   1 = NAND/NOR
  //   Grupo NAND / NOR
  //   Grupo AND / OR
endmodule

module Ex4 (
  input  [1:0] in_1,
  input  [1:0] in_2,
  input  [1:0] in_3,
  input  [1:0] in_4,
  input  [1:0] Seletor,
  input  [1:0] A,
  input  [1:0] B,
  output [1:0] out_8,
  output [1:0] out_9
);

  wire [1:0] and_1_out, and_2_out, nor_1_out, undriven;

  assign and_1_out = Seletor & in_1;  // AND_Gate and_1, 2 bits wide
  assign and_2_out = Seletor & in_2;  // AND_Gate and_2, 2 bits wide
  // NOR_Gate nor_1 has open pins: out=nor_1_out
  assign out_8 = and_1_out | undriven;  // OR_Gate or_1, 2 bits wide
  assign out_9 = and_2_out | nor_1_out;  // OR_Gate or_2, 2 bits wide
  // OR_Gate or_3 is placed but not wired
  // XOR_Gate xor_1 is placed but not wired
  // XNOR_Gate xnor_1 is placed but not wired
  // AND_Gate and_3 is placed but not wired
endmodule

module tmp (
  input  [1:0] \or ,
  input  [1:0] \nor ,
  input  [1:0] \xor ,
  input  [1:0] \xnor ,
  input  in_5,
  input  in_6,
  output [1:0] out_7
);

  wire [1:0] and_1_out, and_2_out, and_3_out, and_4_out, or_1_out, or_2_out;
  wire [1:1] not_1_out;

  not not_1 (not_1_out[1], in_6);
  assign and_1_out = \or  & {2{not_1_out[1]}};  // AND_Gate and_1, 2 bits wide
  assign and_2_out = \nor  & {2{not_1_out[1]}};  // AND_Gate and_2, 2 bits wide
  assign and_3_out = \xor  & {2{in_6}};  // AND_Gate and_3, 2 bits wide
  assign and_4_out = \xnor  & {2{in_6}};  // AND_Gate and_4, 2 bits wide
  assign or_1_out = and_1_out | and_2_out;  // OR_Gate or_1, 2 bits wide
  assign or_2_out = and_3_out | and_4_out;  // OR_Gate or_2, 2 bits wide
  assign out_7 = or_1_out | or_2_out;  // OR_Gate or_3, 2 bits wide
endmodule
