// Logisim project Exemplo0031.circ as structural Verilog: 1 circuit, main circuit main
module main (
  input  [3:0] a,
  input  [3:0] b,
  output [3:0] s1,
  output [3:0] s2
);

  assign s1 = b;  // AND_Gate and, 4 bits wide AND_Gate
  assign s2 = b | a;  // OR_Gate or, 4 bits wide

  // Notes on the sheet:
  //   Alvaro Henrique de Araujo Rungue - 395487
endmodule
