// Logisim project Exemplo0032.circ as structural Verilog: 2 circuits, main circuit main
// Nome
module main (
  input  [1:0] a,
  input  [1:0] b,
  input  Seletor_FLAG,
  output [1:0] out_4
);

  wire [1:0] and_1_out, and_2_out, andeor_1_s1, andeor_1_s2, not_1_out;

  andEor andeor_1 (.a(a), .b(b), .s1(andeor_1_s1), .s2(andeor_1_s2));
  // Probe on Seletor_FLAG
  assign not_1_out = ~{2{Seletor_FLAG}};  // NOT_Gate not_1, 2 bits wide
  // Probe on Seletor_FLAG
  assign and_1_out = andeor_1_s1 & {2{Seletor_FLAG}};  // AND_Gate and_1, 2 bits wide
  assign and_2_out = andeor_1_s2 & not_1_out;  // AND_Gate and_2, 2 bits wide
  assign out_4 = and_1_out | and_2_out;  // OR_Gate or_1, 2 bits wide

  // Notes on the sheet:
  //   00 = OR
  //   11 = AND
  //   Alvaro Henrique de Araujo Rungue - 395487
endmodule

// EX0031(2bits)
module andEor (
  input  [1:0] a,
  input  [1:0] b,
  output [1:0] s1,
  output [1:0] s2
);

  assign s1 = a & b;  // AND_Gate and, 2 bits wide
  assign s2 = b | a;  // OR_Gate or, 2 bits wide

  // Notes on the sheet:
  //   Alvaro Henrique de Araujo Rungue - 395487
endmodule
