// Logisim project Exemplo0033.circ as structural Verilog: 3 circuits, main circuit main
module main (
  input  [1:0] a,
  input  [1:0] b,
  input  in_3,
  output [1:0] s1,
  output [1:0] s2
);

  wire [1:0] AND1_out, AND2_out, AND3_out, AND4_out, andOR1_s1, andOR1_s2, Nand_Nor_s1, Nand_Nor_s2,
       not_1_out, not_2_out;

  andOR andOR1 (.a(a), .b(b), .s1(andOR1_s1), .s2(andOR1_s2));
  nandNor Nand_Nor (.a(a), .b(b), .s1(Nand_Nor_s1), .s2(Nand_Nor_s2));
  // Probe on in_3
  // Probe on in_3
  assign not_1_out = ~{2{in_3}};  // NOT_Gate not_1, 2 bits wide
  assign not_2_out = ~{2{in_3}};  // NOT_Gate not_2, 2 bits wide
  assign AND1_out = andOR1_s1 & not_1_out;  // AND_Gate AND1, 2 bits wide
  assign AND2_out = andOR1_s2 & not_2_out;  // AND_Gate AND2, 2 bits wide
  assign AND3_out = Nand_Nor_s1 & {2{in_3}};  // AND_Gate AND3, 2 bits wide
  assign AND4_out = Nand_Nor_s2 & {2{in_3}};  // AND_Gate AND4, 2 bits wide
  assign s1 = AND1_out | AND3_out;  // OR_Gate or_1, 2 bits wide
  assign s2 = AND2_out | AND4_out;  // OR_Gate or_2, 2 bits wide

  // Notes on the sheet:
  //   Alvaro Henrique de Araujo Rungue - 395487
endmodule

module andOR (
  input  [1:0] a,
  input  [1:0] b,
  output [1:0] s1,
  output [1:0] s2
);

  assign s1 = a & b;  // AND_Gate and, 2 bits wide
  assign s2 = b | a;  // OR_Gate or, 2 bits wide

  // Notes on the sheet:
  //   Alvaro Henrique de Araujo Rungue - 395487
endmodule

module nandNor (
  input  [1:0] a,
  input  [1:0] b,
  output [1:0] s1,
  output [1:0] s2
);

  assign s1 = ~(a & b);  // NAND_Gate nand_1, 2 bits wide
  assign s2 = ~(b | a);  // NOR_Gate nor_1, 2 bits wide

  // Notes on the sheet:
  //   Alvaro Henrique de Araujo Rungue - 395487
endmodule
