// Logisim project Exemplo0034.circ as structural Verilog: 3 circuits, main circuit main
module main (
  input  [1:0] a,
  input  [1:0] b,
  input  [1:0] Flag,
  output [1:0] s1,
  output [1:0] s2
);

  wire [1:0] and_1_out, and_2_out, and_3_out, and_4_out, not_1_out, not_2_out, OR_NOR_s1, OR_NOR_s2,
       XOR_XNOR_s1, XOR_XNOR_s2;

  XORXNOR XOR_XNOR (.a(a), .b(b), .s1(XOR_XNOR_s1), .s2(XOR_XNOR_s2));
  ORNOR OR_NOR (.a(a), .b(b), .s1(OR_NOR_s1), .s2(OR_NOR_s2));
  assign not_1_out = ~Flag;  // NOT_Gate not_1, 2 bits wide
  assign not_2_out = ~Flag;  // NOT_Gate not_2, 2 bits wide
  assign and_1_out = XOR_XNOR_s1 & not_1_out;  // AND_Gate and_1, 2 bits wide
  assign and_2_out = XOR_XNOR_s2 & not_2_out;  // AND_Gate and_2, 2 bits wide
  assign and_3_out = OR_NOR_s1 & Flag;  // AND_Gate and_3, 2 bits wide
  assign and_4_out = OR_NOR_s2 & Flag;  // AND_Gate and_4, 2 bits wide
  assign s1 = and_1_out | and_3_out;  // OR_Gate OR, 2 bits wide
  assign s2 = and_2_out | and_4_out;  // OR_Gate OR2, 2 bits wide

  // Notes on the sheet:
  //   XOR / OR
  //   XNOR / NOR
endmodule

module ORNOR (
  input  [1:0] a,
  input  [1:0] b,
  output [1:0] s1,
  output [1:0] s2
);

  assign s1 = a | b;  // OR_Gate OR, 2 bits wide
  assign s2 = ~(b | a);  // NOR_Gate NOR, 2 bits wide

  // Notes on the sheet:
  //   Alvaro Henrique de Araujo Rungue - 395487
endmodule

module XORXNOR (
  input  [1:0] a,
  input  [1:0] b,
  output [1:0] s1,
  output [1:0] s2
);

  assign s1 = a ^ b;  // XOR_Gate XOR, 2 bits wide
  assign s2 = ~(b ^ a);  // XNOR_Gate XNOR, 2 bits wide

  // Notes on the sheet:
  //   Alvaro Henrique de Araujo Rungue - 395487
endmodule
