// Logisim project Exemplo0035.circ as structural Verilog: 1 circuit, main circuit main
module main (
  input  in_1,
  input  in_2,
  output s1,
  output s2,
  output s3,
  output s4,
  output s5,
  output s6,
  output s7,
  output s8
);

  not not_1 (s1, in_1);
  not not_2 (s2, in_2);
  or or_1 (s3, in_1, in_2);
  nor nor_1 (s4, in_1, in_2);
  and and_1 (s5, in_1, in_2);
  nand nand_1 (s6, in_1, in_2);
  xor xor_1 (s7, in_1, in_2);
  xnor xnor_1 (s8, in_1, in_2);

  // Notes on the sheet:
  //   Alvaro Henrique de Araujo Rungue - 395487
endmodule
