// Logisim project Exemplo0032.circ as structural Verilog: 2 circuits, main circuit main
module main (
  input  [1:0] a,
  input  [1:0] b,
  input  _0__OR____1__AND,
  output [1:0] s0
);

  wire [1:0] and_1_out, or_1_out;

  // Probe on or_1_out
  assign or_1_out = b | a;  // OR_Gate or_1, 2 bits wide
  // Probe on and_1_out
  assign and_1_out = b & a;  // AND_Gate and_1, 2 bits wide
  chave chave_1 (.in_2(or_1_out), .in_3(and_1_out), .out_4(s0), .chave(_0__OR____1__AND));
endmodule

// CHAVE
module chave (
  input  chave,
  input  [1:0] in_2,
  input  [1:0] in_3,
  output [1:0] out_4
);

  wire [1:0] and_1_out, and_2_out, not_1_out;

  assign and_1_out = in_2 & not_1_out;  // AND_Gate and_1, 2 bits wide
  assign not_1_out = ~{2{chave}};  // NOT_Gate not_1, 2 bits wide
  assign and_2_out = in_3 & {2{chave}};  // AND_Gate and_2, 2 bits wide
  // Probe on and_1_out
  // Probe on and_2_out
  assign out_4 = and_1_out ^ and_2_out;  // XOR_Gate xor_1, 2 bits wide
endmodule
