// Logisim project Exemplo0033.circ as structural Verilog: 2 circuits, main circuit main
module main (
  input  [1:0] in_1,
  input  [1:0] in_2,
  input  _0_OR_AND____1_NOR_NAND,
  output [1:0] out_4,
  output [1:0] out_5
);

  wire [3:0] nor_1_out, or_1_out;

  or or_1 (or_1_out[0], in_2[0], in_1[0]);
  or or_2 (or_1_out[1], in_2[1], in_1[1]);
  and and_1 (or_1_out[2], in_2[0], in_1[0]);
  and and_2 (or_1_out[3], in_2[1], in_1[1]);
  nor nor_1 (nor_1_out[0], in_2[0], in_1[0]);
  nor nor_2 (nor_1_out[1], in_2[1], in_1[1]);
  nand nand_1 (nor_1_out[2], in_2[0], in_1[0]);
  nand nand_2 (nor_1_out[3], in_2[1], in_1[1]);
  chave chave_1 (
    .s0(out_4), .s1(out_5), .key(_0_OR_AND____1_NOR_NAND), .a___b_____a___b(or_1_out),
    .a____b_____a____b(nor_1_out));
endmodule

// Chave
module chave (
  input  key,
  input  [3:0] a___b_____a___b,
  input  [3:0] a____b_____a____b,
  output [1:0] s0,
  output [1:0] s1
);

  wire [1:0] and_1_out, and_2_out, and_3_out, and_4_out, not_1_out;

  assign not_1_out = ~{2{key}};  // NOT_Gate not_1, 2 bits wide
  // Probe on and_1_out
  assign and_1_out = a___b_____a___b[1:0] & not_1_out;  // AND_Gate and_1, 2 bits wide
  assign and_2_out = a___b_____a___b[3:2] & not_1_out;  // AND_Gate and_2, 2 bits wide
  // Probe on and_2_out
  // Probe on and_3_out
  assign and_3_out = a____b_____a____b[1:0] & {2{key}};  // AND_Gate and_3, 2 bits wide
  assign and_4_out = a____b_____a____b[3:2] & {2{key}};  // AND_Gate and_4, 2 bits wide
  // Probe on and_4_out
  assign s0 = and_1_out ^ and_3_out;  // XOR_Gate xor_1, 2 bits wide
  assign s1 = and_2_out ^ and_4_out;  // XOR_Gate xor_2, 2 bits wide

  // Notes on the sheet:
  //   sinal buffer
  //   sinal negado
  //   w1
  //   w0
  //   w2
  //   w3
endmodule
