// Logisim project Exercicio0035.circ as structural Verilog: 2 circuits, main circuit main
module chave (
  input  [2:0] chave,
  input  [1:0] a,
  input  [1:0] b,
  output [1:0] s
);

  wire [1:0] and_1_out, and_2_out, and_3_out, and_4_out, and_5_out, and_6_out, and_7_out, and_8_out,
       and_9_out, not_1_out, not_2_out, not_3_out, not_4_out, not_5_out, or_1_out, xor_1_out;
  wire [1:1] not_6_out, not_7_out, not_8_out;

  assign not_1_out = ~a;  // NOT_Gate not_1, 2 bits wide
  assign not_2_out = ~b;  // NOT_Gate not_2, 2 bits wide
  assign or_1_out = a | b;  // OR_Gate or_1, 2 bits wide
  assign and_1_out = a & b;  // AND_Gate and_1, 2 bits wide
  assign xor_1_out = b ^ a;  // XOR_Gate xor_1, 2 bits wide
  assign not_3_out = ~or_1_out;  // NOT_Gate not_3, 2 bits wide
  assign not_4_out = ~and_1_out;  // NOT_Gate not_4, 2 bits wide
  assign not_5_out = ~xor_1_out;  // NOT_Gate not_5, 2 bits wide
  not not_6 (not_6_out[1], chave[2]);
  not not_7 (not_7_out[1], chave[0]);
  not not_8 (not_8_out[1], chave[1]);
  assign and_2_out = not_1_out & {2{not_6_out[1]}} & {2{not_8_out[1]}} & {2{not_7_out[1]}};  // AND_Gate and_2, 2 bits wide
  assign and_3_out = not_2_out & {2{not_6_out[1]}} & {2{not_8_out[1]}} & {2{chave[0]}};  // AND_Gate and_3, 2 bits wide
  assign and_4_out = or_1_out & {2{not_6_out[1]}} & {2{chave[1]}} & {2{not_7_out[1]}};  // AND_Gate and_4, 2 bits wide
  assign and_5_out = not_3_out & {2{not_6_out[1]}} & {2{chave[1]}} & {2{chave[0]}};  // AND_Gate and_5, 2 bits wide
  assign and_6_out = and_1_out & {2{chave[2]}} & {2{not_8_out[1]}} & {2{not_7_out[1]}};  // AND_Gate and_6, 2 bits wide
  assign and_7_out = not_4_out & {2{chave[2]}} & {2{not_8_out[1]}} & {2{chave[0]}};  // AND_Gate and_7, 2 bits wide
  assign and_8_out = xor_1_out & {2{chave[2]}} & {2{chave[1]}} & {2{not_7_out[1]}};  // AND_Gate and_8, 2 bits wide
  assign and_9_out = not_5_out & {2{chave[2]}} & {2{chave[1]}} & {2{chave[0]}};  // AND_Gate and_9, 2 bits wide
  assign s = and_2_out | and_3_out | and_4_out | and_5_out | and_6_out | and_7_out | and_8_out | and_9_out;  // OR_Gate or_2, 2 bits wide

  // Notes on the sheet:
  //   s0
  //   s1
  //   s2
  //   s4
  //   s6
  //   s3
  //   s5
  //   s7
endmodule

module main (
  input  [2:0] seletor,
  input  [1:0] a,
  input  [1:0] b,
  output [1:0] out_4
);

  chave chave_1 (.s(out_4), .a(a), .b(b), .chave(seletor));

  // Notes on the sheet:
  //   0 - not a
  //   1 - not b
  //   2 - or
  //   3 - nor
  //   Código das operações
  //   4 - and
  //   5 - nand
  //   6 - xor
  //   7 - xnor
endmodule
