// Logisim project 31.circ as structural Verilog: 1 circuit, main circuit main
module main (
  input  a,
  input  b,
  input  c,
  input  d,
  input  c1,
  input  c2,
  output s
);

  wire and_1_out, and_2_out, and_3_out, and_4_out, not_1_out, not_2_out, not_3_out, not_4_out;

  not not_1 (not_1_out, c1);
  not not_2 (not_2_out, c2);
  not not_3 (not_3_out, c1);
  not not_4 (not_4_out, c2);
  and and_1 (and_1_out, a, not_1_out, not_2_out);
  and and_2 (and_2_out, b, not_3_out, c2);
  and and_3 (and_3_out, c, c1, not_4_out);
  and and_4 (and_4_out, d, c1, c2);
  or or_1 (s, and_1_out, and_2_out, and_3_out, and_4_out);
endmodule
