// Logisim project 33.circ as structural Verilog: 1 circuit, main circuit main
module main (
  input  a,
  input  b,
  input  c,
  input  se,
  output s
);

  wire and_1_out, and_2_out, and_3_out, and_4_out, not_1_out, not_2_out, not_3_out, not_4_out;

  not not_1 (not_1_out, c);
  and and_1 (and_1_out, b, not_1_out, se);
  and and_2 (and_2_out, b, c, not_2_out);
  not not_2 (not_2_out, se);
  not not_3 (not_3_out, c);
  and and_3 (and_3_out, a, not_3_out, not_4_out);
  not not_4 (not_4_out, se);
  and and_4 (and_4_out, a, c, se);
  or or_1 (s, and_1_out, and_2_out, and_3_out, and_4_out);
endmodule
