// Logisim project 34.circ as structural Verilog: 1 circuit, main circuit main
module main (
  input  a,
  input  b,
  input  c1,
  input  c2,
  output s
);

  wire and_1_out, and_2_out, and_3_out, and_4_out, and_5_out, not_1_out, not_2_out, not_3_out, not_4_out,
       not_5_out, not_6_out, not_7_out, not_8_out;

  not not_1 (not_1_out, a);
  not not_2 (not_2_out, b);
  and and_1 (and_1_out, not_1_out, not_2_out, c2);
  not not_3 (not_3_out, a);
  and and_2 (and_2_out, not_3_out, b, not_4_out);
  not not_4 (not_4_out, c2);
  not not_5 (not_5_out, b);
  and and_3 (and_3_out, a, not_5_out, not_6_out);
  not not_6 (not_6_out, c2);
  not not_7 (not_7_out, c1);
  and and_4 (and_4_out, a, not_7_out, not_8_out);
  not not_8 (not_8_out, c2);
  and and_5 (and_5_out, a, b, c1, c2);
  or or_1 (s, and_1_out, and_2_out, and_3_out, and_4_out, and_5_out);
endmodule
