// Logisim project 32.circ as structural Verilog: 1 circuit, main circuit main
module main (
  input  a,
  input  b,
  input  c,
  output s
);

  wire and_1_out, and_2_out, not_1_out;

  not not_1 (not_1_out, c);
  and and_1 (and_1_out, a, not_1_out);
  and and_2 (and_2_out, b, c);
  or or_1 (s, and_1_out, and_2_out);
endmodule
