// Logisim project Exemplo0032.circ as structural Verilog: 2 circuits, main circuit mux
module mux (
  input  x,
  input  y,
  input  chave,
  output s
);

  wire AND1_out, AND2_out, NOT1_out;

  not NOT1 (NOT1_out, chave);
  and AND1 (AND1_out, x, chave);
  and AND2 (AND2_out, NOT1_out, y);
  or OR1 (s, AND1_out, AND2_out);

  // Notes on the sheet:
  //   0 = Y
  //   0 = X
endmodule

module main (
  input  a,
  input  b,
  input  chave2,
  output s1
);

  wire AND1_out, OR1_out;

  and AND1 (AND1_out, a, b);
  or OR1 (OR1_out, a, b);
  mux mux (.x(AND1_out), .y(OR1_out), .chave(chave2), .s(s1));

  // Notes on the sheet:
  //   0 = OR
  //   1 = AND
endmodule
