// Logisim project Exemplo0033.circ as structural Verilog: 2 circuits, main circuit mux
module mux (
  input  x,
  input  y,
  input  z,
  input  w,
  input  chave1,
  output s1,
  output s2
);

  wire AND1_out, AND2_out, AND3_out, AND4_out, NOT1_out, NOT2_out;

  not NOT1 (NOT1_out, chave1);
  not NOT2 (NOT2_out, chave1);
  and AND1 (AND1_out, x, chave1);
  and AND2 (AND2_out, y, NOT1_out);
  and AND3 (AND3_out, z, chave1);
  and AND4 (AND4_out, w, NOT2_out);
  or OR1 (s1, AND1_out, AND2_out);
  or OR2 (s2, AND3_out, AND4_out);

  // Notes on the sheet:
  //   1 = X e Z
  //   0 = Y e W
endmodule

module main (
  input  a,
  input  b,
  input  chave2,
  output s3,
  output s4
);

  wire AND1_out, NAND1_out, NOR1_out, OR1_out;

  nor NOR1 (NOR1_out, a, b);
  or OR1 (OR1_out, b, a);
  nand NAND1 (NAND1_out, a, b);
  and AND1 (AND1_out, a, b);
  mux mux (.x(NOR1_out), .y(OR1_out), .z(NAND1_out), .w(AND1_out), .chave1(chave2), .s1(s3), .s2(s4));

  // Notes on the sheet:
  //   0 = OR e AND
  //   1 = NOR e NAND
endmodule
