// Logisim project Exemplo0034.circ as structural Verilog: 2 circuits, main circuit mux
module mux (
  input  x,
  input  y,
  input  z,
  input  w,
  input  [1:0] chave1,
  output s1,
  output s2
);

  wire AND1_out, AND2_out, AND3_out, AND4_out, NOT1_out, NOT2_out, NOT3_out, NOT4_out;

  not NOT1 (NOT1_out, chave1[1]);
  not NOT2 (NOT2_out, chave1[0]);
  not NOT3 (NOT3_out, chave1[0]);
  not NOT4 (NOT4_out, chave1[1]);
  and AND1 (AND1_out, x, NOT1_out, NOT2_out);
  and AND2 (AND2_out, y, chave1[1], NOT3_out);
  and AND3 (AND3_out, z, NOT4_out, chave1[0]);
  and AND4 (AND4_out, w, chave1[0], chave1[1]);
  or OR1 (s1, AND1_out, AND2_out);
  or OR2 (s2, AND3_out, AND4_out);

  // Notes on the sheet:
  //   00 = X
  //   01 = Z
  //   10 = Y
  //   11 = W
endmodule

module main (
  input  a,
  input  b,
  input  [1:0] chave2,
  output s3,
  output s4
);

  wire NOR1_out, OR1_out, XNOR1_out, XOR1_out;

  or OR1 (OR1_out, a, b);
  xor XOR1 (XOR1_out, a, b);
  nor NOR1 (NOR1_out, a, b);
  xnor XNOR1 (XNOR1_out, a, b);
  mux mux (.x(OR1_out), .y(XOR1_out), .z(NOR1_out), .w(XNOR1_out), .chave1(chave2), .s1(s3), .s2(s4));

  // Notes on the sheet:
  //   00 = OR
  //   01 = NOR
  //   10 = XOR
  //   11= XNOR
endmodule
