// Logisim project Exemplo0035.circ as structural Verilog: 2 circuits, main circuit mux
module mux (
  input  x,
  input  y,
  input  z,
  input  w,
  input  a,
  input  b,
  input  c,
  input  d,
  input  [2:0] chave1,
  output s1
);

  wire AND1_out, AND2_out, AND3_out, AND4_out, AND5_out, AND6_out, AND7_out, AND8_out, not_1_out, not_2_out,
       not_3_out, not_4_out, not_5_out, not_6_out, not_7_out, not_8_out, not_9_out, not_10_out, not_11_out,
       not_12_out;

  not not_1 (not_1_out, chave1[2]);
  not not_2 (not_2_out, chave1[1]);
  not not_3 (not_3_out, chave1[0]);
  not not_4 (not_4_out, chave1[2]);
  not not_5 (not_5_out, chave1[1]);
  not not_6 (not_6_out, chave1[2]);
  not not_7 (not_7_out, chave1[0]);
  not not_8 (not_8_out, chave1[2]);
  not not_9 (not_9_out, chave1[1]);
  not not_10 (not_10_out, chave1[0]);
  not not_11 (not_11_out, chave1[1]);
  not not_12 (not_12_out, chave1[0]);
  and AND1 (AND1_out, x, not_1_out, not_2_out, not_3_out);
  and AND2 (AND2_out, y, not_4_out, not_5_out, chave1[0]);
  and AND3 (AND3_out, z, not_6_out, chave1[1], not_7_out);
  and AND4 (AND4_out, w, not_8_out, chave1[1], chave1[0]);
  and AND5 (AND5_out, a, chave1[2], not_9_out, not_10_out);
  and AND6 (AND6_out, b, chave1[2], not_11_out, chave1[0]);
  and AND7 (AND7_out, c, chave1[2], chave1[1], not_12_out);
  and AND8 (AND8_out, d, chave1[2], chave1[1], chave1[0]);
  or OR1 (s1, AND1_out, AND2_out, AND3_out, AND4_out, AND5_out, AND6_out, AND7_out, AND8_out);

  // Notes on the sheet:
  //   000 = X
  //   001 = Y
  //   010 = Z
  //   011 = W
  //   100 = A
  //   101 = B
  //   110 = C
  //   111 = D
endmodule

module main (
  input  a,
  input  b,
  input  [2:0] chave2,
  output s2
);

  wire AND1_out, NAND1_out, NOR1_out, NOTA_out, NOTB_out, OR1_out, XNOR1_out, XOR1_out;

  or OR1 (OR1_out, a, b);
  xor XOR1 (XOR1_out, a, b);
  nor NOR1 (NOR1_out, a, b);
  xnor XNOR1 (XNOR1_out, a, b);
  and AND1 (AND1_out, a, b);
  nand NAND1 (NAND1_out, a, b);
  not NOTA (NOTA_out, a);
  not NOTB (NOTB_out, b);
  mux mux (
    .x(OR1_out), .y(XOR1_out), .z(NOR1_out), .w(XNOR1_out), .a(AND1_out), .b(NAND1_out), .c(NOTA_out),
    .d(NOTB_out), .chave1(chave2), .s1(s2));

  // Notes on the sheet:
  //   000 = OR
  //   001 = XOR
  //   010 = NOR
  //   011 = XNOR
  //   100 = AND
  //   101 = NAND
  //   110 = NOTA
  //   111 = NOTB
endmodule
