// Logisim project Exemplo0031.circ as structural Verilog: 1 circuit, main circuit main
module main (
  input  a,
  input  b,
  input  c,
  input  d,
  output s1,
  output s2
);

  and AND1 (s1, d, c, b, a);
  or OR1 (s2, d, c, b, a);
endmodule
