// Logisim project Exemplo0032.circ as structural Verilog: 2 circuits, main circuit main
module main (
  input  a,
  input  b,
  input  Chave,
  output s
);

  wire AND1_out, OR1_out;

  and AND1 (AND1_out, a, b);
  or OR1 (OR1_out, a, b);
  MUX mux_1 (.e1(AND1_out), .e2(OR1_out), .c1(Chave), .s1(s));

  // Notes on the sheet:
  //   0 - OR
  //   1 - AND
endmodule

module MUX (
  input  e1,
  input  e2,
  input  c1,
  output s1
);

  wire AND1_out, AND2_out, NOT1_out;

  not NOT1 (NOT1_out, c1);
  and AND1 (AND1_out, e1, c1);
  and AND2 (AND2_out, NOT1_out, e2);
  or OR1 (s1, AND1_out, AND2_out);

  // Notes on the sheet:
  //   0 - e2
  //   1- e1
endmodule
