// Logisim project Exemplo0033.circ as structural Verilog: 2 circuits, main circuit main
module main (
  input  a,
  input  b,
  input  _0___OR_AND,
  output x___w,
  output z___y
);

  wire w_out, x_out, y_out, z_out;

  nand w (w_out, a, b);
  and x (x_out, a, b);
  nor y (y_out, a, b);
  or z (z_out, a, b);
  MUX mux_1 (.e1(w_out), .e2(x_out), .e3(y_out), .e4(z_out), .c1(_0___OR_AND), .s1(x___w), .s2(z___y));

  // Notes on the sheet:
  //   1- NOR/NAND
endmodule

module MUX (
  input  e1,
  input  e2,
  input  e3,
  input  e4,
  input  c1,
  output s1,
  output s2
);

  wire AND1_out, AND2_out, AND3_out, AND4_out, not_1_out, not_2_out;

  not not_1 (not_1_out, c1);
  not not_2 (not_2_out, c1);
  and AND1 (AND1_out, e1, c1);
  and AND2 (AND2_out, e2, not_1_out);
  and AND3 (AND3_out, e3, c1);
  and AND4 (AND4_out, e4, not_2_out);
  or OR1 (s1, AND1_out, AND2_out);
  or OR2 (s2, AND3_out, AND4_out);
endmodule
