// Logisim project Exemplo0034.circ as structural Verilog: 2 circuits, main circuit main
module main (
  input  a,
  input  b,
  input  [1:0] Chave,
  output s
);

  wire NOR1_out, OR1_out, XNOR1_out, XOR_out;

  or OR1 (OR1_out, a, b);
  nor NOR1 (NOR1_out, a, b);
  xor XOR (XOR_out, a, b);
  xnor XNOR1 (XNOR1_out, a, b);
  MUX mux_1 (.e1(OR1_out), .e2(NOR1_out), .e3(XOR_out), .e4(XNOR1_out), .C1(Chave), .s1(s));

  // Notes on the sheet:
  //   00 - OR
  //   01 - NOR
  //   10 - XOR
  //   11 - XNOR
endmodule

module MUX (
  input  e1,
  input  e2,
  input  e3,
  input  e4,
  input  [1:0] C1,
  output s1
);

  wire AND1_out, AND2_out, AND3_out, AND4_out, not_1_out, not_2_out, not_3_out, not_4_out;

  not not_1 (not_1_out, C1[1]);
  not not_2 (not_2_out, C1[0]);
  not not_3 (not_3_out, C1[1]);
  not not_4 (not_4_out, C1[0]);
  and AND1 (AND1_out, e1, not_1_out, not_2_out);
  and AND2 (AND2_out, e2, not_3_out, C1[0]);
  and AND3 (AND3_out, e3, C1[1], not_4_out);
  and AND4 (AND4_out, e4, C1[1], C1[0]);
  or OR1 (s1, AND1_out, AND2_out, AND3_out, AND4_out);
endmodule
