// Logisim project Exemplo0035.circ as structural Verilog: 2 circuits, main circuit main
module main (
  input  a,
  input  b,
  input  [2:0] CHAVE,
  output s
);

  wire AND1_out, NAND1_out, NOR1_out, NOT__a_out, NOT__b_out, OR1_out, XNOR1_out, XOR_out;

  not NOT__b (NOT__b_out, b);
  or OR1 (OR1_out, b, a);
  nor NOR1 (NOR1_out, b, a);
  and AND1 (AND1_out, b, a);
  nand NAND1 (NAND1_out, b, a);
  xor XOR (XOR_out, b, a);
  xnor XNOR1 (XNOR1_out, b, a);
  not NOT__a (NOT__a_out, a);
  MUX mux_1 (
    .e1(NOT__b_out), .e2(OR1_out), .e3(NOR1_out), .e4(AND1_out), .e5(NAND1_out), .e6(XOR_out),
    .e7(XNOR1_out), .e8(NOT__a_out), .C1(CHAVE), .s1(s));

  // Notes on the sheet:
  //   001 - OR
  //   010 - NOR
  //   011 - AND
  //   101 - XOR
  //   110 - XNOR
  //   000 - NOT(b)
  //   100 - NAND
  //   111 - NOT(a)
endmodule

module MUX (
  input  e1,
  input  e2,
  input  e3,
  input  e4,
  input  e5,
  input  e6,
  input  e7,
  input  e8,
  input  [2:0] C1,
  output s1
);

  wire AND1_out, AND2_out, AND3_out, AND4_out, AND5_out, AND7_out, AND8_out, AND_6_out, not_1_out, not_2_out,
       not_3_out, not_4_out, not_5_out, not_6_out, not_7_out, not_8_out, not_9_out, not_10_out, not_11_out,
       not_12_out;

  not not_1 (not_1_out, C1[2]);
  not not_2 (not_2_out, C1[1]);
  not not_3 (not_3_out, C1[0]);
  not not_4 (not_4_out, C1[2]);
  not not_5 (not_5_out, C1[1]);
  not not_6 (not_6_out, C1[2]);
  not not_7 (not_7_out, C1[0]);
  not not_8 (not_8_out, C1[2]);
  not not_9 (not_9_out, C1[1]);
  not not_10 (not_10_out, C1[0]);
  not not_11 (not_11_out, C1[1]);
  not not_12 (not_12_out, C1[0]);
  and AND1 (AND1_out, e1, not_1_out, not_2_out, not_3_out);
  and AND2 (AND2_out, e2, not_4_out, not_5_out, C1[0]);
  and AND3 (AND3_out, e3, not_6_out, C1[1], not_7_out);
  and AND4 (AND4_out, e4, not_8_out, C1[1], C1[0]);
  and AND5 (AND5_out, e5, C1[2], not_9_out, not_10_out);
  and AND_6 (AND_6_out, e6, C1[2], not_11_out, C1[0]);
  and AND7 (AND7_out, e7, C1[2], C1[1], not_12_out);
  and AND8 (AND8_out, e8, C1[2], C1[1], C1[0]);
  or OR1 (s1, AND1_out, AND2_out, AND3_out, AND4_out, AND5_out, AND_6_out, AND7_out, AND8_out);
endmodule
