// Logisim project Exemplo0036.circ as structural Verilog: 2 circuits, main circuit main
// Mlt
module main (
  input  [3:0] a,
  input  [3:0] b,
  input  c,
  output [3:0] S
);

  wire [3:0] and_1_out, and_2_out, not_1_out;

  assign not_1_out = ~{4{c}};  // NOT_Gate not_1, 4 bits wide
  assign and_1_out = a & {4{c}};  // AND_Gate and_1, 4 bits wide
  assign and_2_out = b & not_1_out;  // AND_Gate and_2, 4 bits wide
  assign S = and_1_out | and_2_out;  // OR_Gate or_1, 4 bits wide
endmodule

module Multiplex (
  input  [3:0] a,
  input  [3:0] b,
  input  C,
  output [3:0] S
);

  wire [3:0] xnor_1_out, xor_1_out;

  assign xnor_1_out = ~(b ^ a);  // XNOR_Gate xnor_1, 4 bits wide
  assign xor_1_out = b ^ a;  // XOR_Gate xor_1, 4 bits wide
  main main_1 (.a(xor_1_out), .b(xnor_1_out), .c(C), .S(S));

  // Notes on the sheet:
  //   0 - igualdade
  //   1 - desigualdade
endmodule
