// Logisim project Exemplo0032.circ as structural Verilog: 2 circuits, main circuit main
module main (
  input  [1:0] in_1,
  input  [1:0] in_2,
  input  in_3,
  output [1:0] out_4
);

  wire [1:0] and_1_out, and_2_out, and_or_1_out_3, and_or_1_out_4, not_1_out;

  and_or and_or_1 (.in_1(in_1), .in_2(in_2), .out_3(and_or_1_out_3), .out_4(and_or_1_out_4));
  // Probe on in_3
  // Probe on in_3
  assign not_1_out = ~{2{in_3}};  // NOT_Gate not_1, 2 bits wide
  assign and_1_out = and_or_1_out_3 & {2{in_3}};  // AND_Gate and_1, 2 bits wide
  assign and_2_out = and_or_1_out_4 & not_1_out;  // AND_Gate and_2, 2 bits wide
  assign out_4 = and_1_out | and_2_out;  // OR_Gate or_1, 2 bits wide
endmodule

module and_or (
  input  [1:0] in_1,
  input  [1:0] in_2,
  output [1:0] out_3,
  output [1:0] out_4
);

  assign out_3 = in_1 & in_2;  // AND_Gate and_1, 2 bits wide
  assign out_4 = in_2 | in_1;  // OR_Gate or_1, 2 bits wide
endmodule
