// Logisim project Exemplo0035.circ as structural Verilog: 2 circuits, main circuit main
module main (
  input  a,
  input  b,
  input  [2:0] CHAVE,
  output s
);

  wire and_1_out, nand_1_out, nor_1_out, not_1_out, not_2_out, or_1_out, xnor_1_out, xor_1_out;

  not not_1 (not_1_out, b);
  not not_2 (not_2_out, a);
  or or_1 (or_1_out, a, b);
  nor nor_1 (nor_1_out, a, b);
  and and_1 (and_1_out, a, b);
  nand nand_1 (nand_1_out, a, b);
  xor xor_1 (xor_1_out, a, b);
  xnor xnor_1 (xnor_1_out, a, b);
  circuito circuito_1 (
    .in_1(not_1_out), .in_2(or_1_out), .in_3(nor_1_out), .in_4(and_1_out), .in_5(nand_1_out),
    .in_6(xor_1_out), .in_7(xnor_1_out), .in_8(not_2_out), .in_9(CHAVE), .out_10(s));
endmodule

module circuito (
  input  in_1,
  input  in_2,
  input  in_3,
  input  in_4,
  input  in_5,
  input  in_6,
  input  in_7,
  input  in_8,
  input  [2:0] in_9,
  output out_10
);

  wire and_1_out, and_2_out, and_3_out, and_4_out, and_5_out, and_6_out, and_7_out, and_8_out, not_1_out,
       not_2_out, not_3_out, not_4_out, not_5_out, not_6_out, not_7_out, not_8_out, not_9_out, not_10_out,
       not_11_out, not_12_out;

  not not_1 (not_1_out, in_1);
  not not_2 (not_2_out, in_9[1]);
  not not_3 (not_3_out, in_9[0]);
  not not_4 (not_4_out, in_1);
  not not_5 (not_5_out, in_9[1]);
  not not_6 (not_6_out, in_1);
  not not_7 (not_7_out, in_9[0]);
  not not_8 (not_8_out, in_1);
  not not_9 (not_9_out, in_9[1]);
  not not_10 (not_10_out, in_9[0]);
  not not_11 (not_11_out, in_9[1]);
  not not_12 (not_12_out, in_9[0]);
  and and_1 (and_1_out, not_1_out, not_2_out, not_3_out);
  and and_2 (and_2_out, in_2, not_4_out, not_5_out, in_9[0]);
  and and_3 (and_3_out, in_3, not_6_out, in_9[1], not_7_out);
  and and_4 (and_4_out, in_4, not_8_out, in_9[1], in_9[0]);
  and and_5 (and_5_out, in_5, in_1, not_9_out, not_10_out);
  and and_6 (and_6_out, in_6, in_1, not_11_out, in_9[0]);
  and and_7 (and_7_out, in_7, in_1, in_9[1], not_12_out);
  and and_8 (and_8_out, in_8, in_1, in_9[1], in_9[0]);
  or or_1 (out_10, and_1_out, and_2_out, and_3_out, and_4_out, and_5_out, and_6_out, and_7_out, and_8_out);

  assign in_9[2] = in_1;
endmodule
