// Logisim project Exemplo0034.circ as structural Verilog: 1 circuit, main circuit main
module main (
  input  A,
  input  B,
  input  c1,
  input  c2,
  output out_5,
  output out_6,
  output out_7,
  output out_8
);

  wire NOR_out, not_1_out, not_2_out, not_3_out, not_4_out, OR_out, XNOR_out, XOR_out;

  xor XOR (XOR_out, B, A);
  xnor XNOR (XNOR_out, B, A);
  nor NOR (NOR_out, B, A);
  or OR (OR_out, B, A);
  not not_1 (not_1_out, c2);
  not not_2 (not_2_out, c1);
  not not_3 (not_3_out, c2);
  not not_4 (not_4_out, c1);
  and and_1 (out_5, XOR_out, c1);
  and and_2 (out_6, XNOR_out, c2);
  and and_3 (out_7, not_2_out, OR_out);
  and and_4 (out_8, not_4_out, NOR_out);
endmodule
