// Logisim project Exemplo0032.circ as structural Verilog: 1 circuit, main circuit main
module main (
  input  b,
  input  a,
  input  chave,
  output out_4
);

  wire and_1_out, and_2_out, and_3_out, not_1_out, or_1_out;

  and and_1 (and_1_out, b, a);
  or or_1 (or_1_out, a, b);
  not not_1 (not_1_out, chave);
  buf and_2 (and_2_out, chave);  // AND_Gate
  and and_3 (and_3_out, or_1_out, not_1_out);
  or or_2 (out_4, and_2_out, and_3_out);

  // Notes on the sheet:
  //   Guia 03 - Exemplo0032
  //   João Henrique Mendes de Oliveira - 392734
endmodule
