// Logisim project Exemplo0034.circ as structural Verilog: 1 circuit, main circuit main
module main (
  input  in_1,
  input  in_2,
  input  in_3,
  output out_4,
  output out_5
);

  wire and_1_out, and_2_out, and_3_out, and_4_out, nor_1_out, not_1_out, not_2_out, or_1_out, xnor_1_out,
       xor_1_out;

  or or_1 (or_1_out, in_2, in_1);
  xor xor_1 (xor_1_out, in_2, in_1);
  nor nor_1 (nor_1_out, in_2, in_1);
  xnor xnor_1 (xnor_1_out, in_2, in_1);
  not not_1 (not_1_out, in_3);
  not not_2 (not_2_out, in_3);
  and and_1 (and_1_out, or_1_out, not_1_out);
  and and_2 (and_2_out, xor_1_out, in_3);
  and and_3 (and_3_out, nor_1_out, not_2_out);
  and and_4 (and_4_out, xnor_1_out, in_3);
  or or_2 (out_4, and_1_out, and_2_out);
  or or_3 (out_5, and_3_out, and_4_out);

  // Notes on the sheet:
  //   Guia 03 - Exemplo0034
  //   João henrique Mendes de Oliveira - 392734
endmodule
