// Logisim project Guia03.circ as structural Verilog: 8 circuits, main circuit LU exemplo031
module LU_exemplo031 (
  input  A,
  input  A1,
  input  B,
  input  B1,
  input  select,
  output S1,
  output S2
);

  wire A___B_2_out, A___B_3_out, A___B_4_out, A___B_out, and_1_out, and_2_out, and_3_out, and_4_out,
       not_1_out, not_2_out;

  and A___B (A___B_out, B, A);
  or A___B_2 (A___B_2_out, B, A);
  and and_1 (and_1_out, A___B_out, select);
  not not_1 (not_1_out, select);
  and and_2 (and_2_out, A___B_2_out, not_1_out);
  or or_1 (S1, and_1_out, and_2_out);
  and A___B_3 (A___B_3_out, B1, A1);
  or A___B_4 (A___B_4_out, B1, A1);
  and and_3 (and_3_out, A___B_3_out, select);
  not not_2 (not_2_out, select);
  and and_4 (and_4_out, A___B_4_out, not_2_out);
  or or_2 (S2, and_3_out, and_4_out);

  // Notes on the sheet:
  //   select=0 >>or
  //                       s elect =1 >> &&
endmodule

module Exemplo031 (
  input  in_1,
  input  in_2,
  input  in_3,
  input  in_4,
  input  in_5,
  input  in_6,
  input  in_7,
  input  in_8,
  input  in_9,
  output out_10,
  output out_11,
  output out_12,
  output out_13
);

  LU_exemplo031 lu_exemplo031_1 (.select(in_9), .A(in_1), .A1(in_2), .B(in_5), .B1(in_6), .S1(out_10), .S2(out_11));
  LU_exemplo031 lu_exemplo031_2 (.select(in_9), .A(in_3), .A1(in_4), .B(in_7), .B1(in_8), .S1(out_12), .S2(out_13));
endmodule

module Exemplo032 (
  input  in_1,
  input  in_2,
  input  in_3,
  input  in_4,
  input  in_5,
  output out_6,
  output out_7
);

  LU_exemplo031 lu_exemplo031_1 (.select(in_5), .A(in_1), .A1(in_2), .B(in_3), .B1(in_4), .S1(out_6), .S2(out_7));
endmodule

module Exemplo033 (
  input  A1,
  input  A2,
  input  A1_2,
  input  A2_2,
  input  select,
  output out_6,
  output out_7,
  output out_8,
  output out_9,
  output out_10,
  output out_11,
  output out_12,
  output out_13
);

  LU__exemplo033 LU_exemplo033 (
    .select(select), .A1(A1_2), .A2(A1), .saida__AND(out_6), .saida__OR(out_8), .saida_NOR(out_10),
    .saida_NAND(out_12));
  LU__exemplo033 LU_exemplo033_2 (
    .select(select), .A1(A2_2), .A2(A2), .saida__AND(out_7), .saida__OR(out_9), .saida_NOR(out_11),
    .saida_NAND(out_13));
endmodule

module LU__exemplo033 (
  input  A1,
  input  A2,
  input  select,
  output saida__AND,
  output saida__OR,
  output saida_NOR,
  output saida_NAND
);

  wire and_1_out, nand_1_out, nor_1_out, not_1_out, not_2_out, or_1_out;

  and and_1 (and_1_out, A2, A1);
  or or_1 (or_1_out, A2, A1);
  nor nor_1 (nor_1_out, A2, A1);
  nand nand_1 (nand_1_out, A2, A1);
  not not_1 (not_1_out, select);
  not not_2 (not_2_out, select);
  and and_2 (saida__AND, and_1_out, not_1_out);
  and and_3 (saida__OR, or_1_out, not_2_out);
  and and_4 (saida_NOR, nor_1_out, select);
  and and_5 (saida_NAND, nand_1_out, select);

  // Notes on the sheet:
  //   select=1 NOR e NAND
  //   select =0 AND e OR
endmodule

module LU_Exemplo034 (
  input  A,
  input  B,
  input  selectA,
  input  select_B,
  output S_or_e_NOR,
  output S_XOR_e_XNOR
);

  wire and_1_out, and_2_out, and_3_out, and_4_out, and_5_out, and_6_out, and_7_out, and_8_out, nor_1_out,
       not_1_out, not_2_out, not_3_out, not_4_out, or_1_out, xnor_1_out, xor_1_out;

  or or_1 (or_1_out, B, A);
  nor nor_1 (nor_1_out, B, A);
  xor xor_1 (xor_1_out, B, A);
  xnor xnor_1 (xnor_1_out, B, A);
  not not_1 (not_1_out, selectA);
  not not_2 (not_2_out, selectA);
  and and_1 (and_1_out, or_1_out, not_1_out);
  and and_2 (and_2_out, nor_1_out, not_2_out);
  and and_3 (and_3_out, xor_1_out, selectA);
  and and_4 (and_4_out, xnor_1_out, selectA);
  not not_3 (not_3_out, select_B);
  not not_4 (not_4_out, select_B);
  and and_5 (and_5_out, and_1_out, not_3_out);
  and and_6 (and_6_out, and_2_out, select_B);
  and and_7 (and_7_out, and_3_out, not_4_out);
  and and_8 (and_8_out, and_4_out, select_B);
  or or_2 (S_XOR_e_XNOR, and_7_out, and_8_out);
  or or_3 (S_or_e_NOR, and_5_out, and_6_out);
endmodule

module Exemplo34 (
  input  A1,
  input  A2,
  input  B1,
  input  B2,
  input  in_5,
  input  in_6,
  output out_7,
  output out_8,
  output out_9,
  output out_10
);

  LU_Exemplo034 lu_exemplo034_1 (
    .selectA(in_5), .select_B(in_6), .A(A1), .B(B1), .S_or_e_NOR(out_9), .S_XOR_e_XNOR(out_7));
  LU_Exemplo034 lu_exemplo034_2 (
    .selectA(in_5), .select_B(in_6), .A(B2), .B(A2), .S_or_e_NOR(out_10), .S_XOR_e_XNOR(out_8));
endmodule

module Exemplo035 (
  input  in_1,
  input  in_2,
  output out_3,
  output out_4,
  output out_5,
  output out_6,
  output out_7,
  output out_8,
  output out_9,
  output out_10
);

  not not_1 (out_3, in_2);
  not not_2 (out_4, in_1);
  and and_1 (out_5, in_2, in_1);
  or or_1 (out_6, in_2, in_1);
  nand nand_1 (out_7, in_2, in_1);
  nor nor_1 (out_8, in_2, in_1);
  xor xor_1 (out_9, in_2, in_1);
  xnor xnor_1 (out_10, in_2, in_1);
endmodule
