// Logisim project circuito Exemplo031.circ as structural Verilog: 2 circuits, main circuit LU
module LU (
  input  A,
  input  A1,
  input  B,
  input  B1,
  input  select,
  output S1,
  output S2
);

  wire A___B_2_out, A___B_3_out, A___B_4_out, A___B_out, and_1_out, and_2_out, and_3_out, and_4_out,
       not_1_out, not_2_out;

  and A___B (A___B_out, B, A);
  or A___B_2 (A___B_2_out, B, A);
  and and_1 (and_1_out, A___B_out, select);
  not not_1 (not_1_out, select);
  and and_2 (and_2_out, A___B_2_out, not_1_out);
  or or_1 (S1, and_1_out, and_2_out);
  and A___B_3 (A___B_3_out, B1, A1);
  or A___B_4 (A___B_4_out, B1, A1);
  and and_3 (and_3_out, A___B_3_out, select);
  not not_2 (not_2_out, select);
  and and_4 (and_4_out, A___B_4_out, not_2_out);
  or or_2 (S2, and_3_out, and_4_out);

  // Notes on the sheet:
  //   select=0 >>or
  //                       s elect =1 >> &&
endmodule

module main (
  input  in_1,
  input  in_2,
  input  in_3,
  input  in_4,
  input  in_5,
  input  in_6,
  input  in_7,
  input  in_8,
  input  in_9,
  output out_10,
  output out_11,
  output out_12,
  output out_13
);

  LU lu_1 (.select(in_9), .A(in_1), .A1(in_2), .B(in_5), .B1(in_6), .S1(out_10), .S2(out_11));
  LU lu_2 (.select(in_9), .A(in_3), .A1(in_4), .B(in_7), .B1(in_8), .S1(out_12), .S2(out_13));
endmodule
