// Logisim project Exemplo0031.circ as structural Verilog: 1 circuit, main circuit main
module main (
  input  [3:0] a,
  input  [3:0] b,
  output [3:0] out_3,
  output [3:0] out_4
);

  assign out_3 = a & b;  // AND_Gate and_1, 4 bits wide
  assign out_4 = a | b;  // OR_Gate or_1, 4 bits wide
endmodule
