// Logisim project Exemplo0032.circ as structural Verilog: 1 circuit, main circuit main
module main (
  input  [1:0] a,
  input  [1:0] b,
  input  [1:0] op,
  output [1:0] out_4
);

  wire [1:0] s1_out, s2_out, s3_out, s4_out;

  assign s4_out = a | b;  // OR_Gate s4, 2 bits wide
  assign s2_out = ~op;  // NOT_Gate s2, 2 bits wide
  assign s3_out = a & b & op;  // AND_Gate s3, 2 bits wide
  assign s1_out = s4_out & s2_out;  // AND_Gate s1, 2 bits wide
  assign out_4 = s1_out | s3_out;  // OR_Gate s, 2 bits wide

  // Notes on the sheet:
  //   0 - OR
  //   1 - AND
endmodule
