// Logisim project Exemplo0033(a).circ as structural Verilog: 1 circuit, main circuit main
module main (
  input  b,
  input  a,
  input  op,
  output OR_NOR,
  output AND_NAND
);

  wire not_1_out, s1_out, s2_out, s3_out, s4_out, s5_out, s6_out, s7_out;

  not not_1 (not_1_out, op);
  or s4 (s4_out, a, b);
  and s5 (s5_out, a, not_1_out, b);
  nor s6 (s6_out, a, b);
  nand s7 (s7_out, a, b);
  and s3 (s3_out, s4_out, not_1_out);
  and s1 (s1_out, s6_out, op);
  and s2 (s2_out, s7_out, s7_out, op);
  or s (OR_NOR, s3_out, s1_out);
  or s0 (AND_NAND, s5_out, s2_out);

  // Notes on the sheet:
  //   0 - OR/AND
  //   1 - NOR/NAND
endmodule
