// Logisim project Exemplo0033(b).circ as structural Verilog: 1 circuit, main circuit main
module main (
  input  a,
  input  b,
  input  op,
  output out_4,
  output out_5
);

  wire s1_out, s2_out;

  or s1 (s1_out, b, a);
  and s2 (s2_out, b, a);
  xor s (out_4, op, s1_out);
  xor s0 (out_5, op, s2_out);

  // Notes on the sheet:
  //   OBS.: Circuito simplificado do Exemplo0033(a).circ
endmodule
