// Logisim project Exemplo0034(a).circ as structural Verilog: 1 circuit, main circuit main
module main (
  input  a,
  input  b,
  input  [1:0] c1c2,
  output out_4
);

  wire not_1_out, not_2_out, not_3_out, not_4_out, s1_out, s2_out, s3_out, s4_out, s5_out, s6_out, s7_out,
       s8_out;

  or s5 (s5_out, b, a);
  nor s6 (s6_out, b, a);
  xor s7 (s7_out, b, a);
  xnor s8 (s8_out, b, a);
  not not_1 (not_1_out, c1c2[1]);
  not not_2 (not_2_out, c1c2[0]);
  not not_3 (not_3_out, c1c2[1]);
  not not_4 (not_4_out, c1c2[0]);
  and s1 (s1_out, not_1_out, s5_out, not_2_out);
  and s2 (s2_out, not_3_out, s6_out, c1c2[0]);
  and s3 (s3_out, c1c2[1], s7_out, not_4_out);
  and s4 (s4_out, c1c2[1], s8_out, c1c2[0]);
  or s (out_4, s1_out, s2_out, s3_out, s4_out);
endmodule
