// Logisim project Exemplo0034(b).circ as structural Verilog: 1 circuit, main circuit main
module main (
  input  a,
  input  b,
  input  [1:0] c1c2,
  output out_4
);

  wire s1_out, s2_out, s3_out, s4_out, s5_out, s6_out, s7_out;

  or s7 (s7_out, b, a);
  xor s6 (s6_out, b, a);
  xor s4 (s4_out, s7_out, c1c2[0]);
  xor s5 (s5_out, s6_out, c1c2[0]);
  not s3 (s3_out, c1c2[1]);
  and s1 (s1_out, s4_out, s3_out);
  and s2 (s2_out, s5_out, c1c2[1]);
  or s (out_4, s1_out, s2_out);

  // Notes on the sheet:
  //   OBS.: Simplificado do circuito Exemplo0034(a).circ
endmodule
