// Logisim project Exemplo0035.circ as structural Verilog: 1 circuit, main circuit main
module main (
  input  a,
  input  b,
  input  c1,
  input  c2,
  input  c3,
  output out_6
);

  wire not_1_out, not_2_out, not_3_out, not_4_out, not_5_out, not_6_out, not_7_out, not_8_out, not_9_out,
       not_10_out, not_11_out, not_12_out, not_13_out, not_14_out, s1_out, s2_out, s3_out, s4_out, s5_out,
       s6_out, s7_out, s8_out, s9_out, s10_out, s11_out, s12_out, s13_out;

  not not_1 (not_1_out, b);
  not not_2 (not_2_out, a);
  or s9 (s9_out, b, a);
  nor s10 (s10_out, b, a);
  nand s11 (s11_out, b, a);
  xor s12 (s12_out, b, a);
  xnor s13 (s13_out, b, a);
  not not_3 (not_3_out, c3);
  not not_4 (not_4_out, c3);
  not not_5 (not_5_out, c2);
  not not_6 (not_6_out, c1);
  not not_7 (not_7_out, c2);
  not not_8 (not_8_out, c1);
  not not_9 (not_9_out, c3);
  not not_10 (not_10_out, c1);
  not not_11 (not_11_out, c1);
  not not_12 (not_12_out, c3);
  not not_13 (not_13_out, c2);
  not not_14 (not_14_out, c2);
  and s1 (s1_out, c3, c2, c1, not_1_out);
  and s2 (s2_out, not_3_out, c2, c1, not_2_out);
  and s3 (s3_out, not_4_out, not_5_out, not_6_out, s9_out);
  and s4 (s4_out, c3, not_7_out, not_8_out, s10_out);
  and s5 (s5_out, not_9_out, c2, not_10_out, b, a);
  and s6 (s6_out, c3, c2, not_11_out, s11_out);
  and s7 (s7_out, not_12_out, not_13_out, c1, s12_out);
  and s8 (s8_out, c3, not_14_out, c1, s13_out);
  or s (out_6, s1_out, s2_out, s3_out, s4_out, s5_out, s6_out, s7_out, s8_out);

  // Notes on the sheet:
  //   000 - OR
  //   001 - NOR
  //   010 - AND
  //   011 - NAND
  //   100 - XOR
  //   101 - XNOR
  //   110 - NOT(a)
  //   111 - NOT(b)
endmodule
