// Logisim project Exemplo0036.circ as structural Verilog: 1 circuit, main circuit main
module main (
  input  a,
  input  b,
  input  chave,
  input  a_2,
  input  b_2,
  output \_0___Não ,
  output \_0___Não_2 
);

  wire and_1_out, and_2_out, and_3_out, and_4_out, not_1_out, not_2_out, xnor_1_out, xnor_2_out, xor_1_out,
       xor_2_out;

  xor xor_1 (xor_1_out, b, a);
  xnor xnor_1 (xnor_1_out, b, a);
  xor xor_2 (xor_2_out, b_2, a_2);
  xnor xnor_2 (xnor_2_out, b_2, a_2);
  not not_1 (not_1_out, chave);
  not not_2 (not_2_out, chave);
  and and_1 (and_1_out, xor_1_out, chave);
  and and_2 (and_2_out, not_1_out, xnor_1_out);
  and and_3 (and_3_out, xor_2_out, chave);
  and and_4 (and_4_out, not_2_out, xnor_2_out);
  or or_1 (\_0___Não , and_1_out, and_2_out);
  or or_2 (\_0___Não_2 , and_3_out, and_4_out);

  // Notes on the sheet:
  //   0 - iguais
  //   1 - diferentes
  //   1 - Sim
  //   1 - Sim
endmodule
