// Logisim project Exemplo0031.circ as structural Verilog: 1 circuit, main circuit main
module main (
  input  [3:0] a,
  input  [3:0] in_2,
  input  [3:0] b,
  input  [3:0] in_4
);

  wire [3:0] and_1_out, or_1_out;

  assign and_1_out = a & b;  // AND_Gate and_1, 4 bits wide
  assign or_1_out = a | b;  // OR_Gate or_1, 4 bits wide
endmodule
