// Logisim project Exemplo0032.circ as structural Verilog: 2 circuits, main circuit main
module main (
  input  [1:0] a,
  input  [1:0] b,
  input  Chave,
  output [1:0] Saida
);

  wire [1:0] and_1_out, or_1_out;

  assign and_1_out = b & a;  // AND_Gate and_1, 2 bits wide
  assign or_1_out = a | b;  // OR_Gate or_1, 2 bits wide
  Multiplexador multiplexador_1 (.\and (and_1_out), .\or (or_1_out), .chave(Chave), .S(Saida));

  // Notes on the sheet:
  //   0-Or
  //            1-And
endmodule

// Multi.
module Multiplexador (
  input  [1:0] \and ,
  input  [1:0] \or ,
  input  chave,
  output [1:0] S
);

  wire [1:0] and_1_out, and_2_out, not_1_out;

  assign not_1_out = ~{2{chave}};  // NOT_Gate not_1, 2 bits wide
  assign and_1_out = \and  & {2{chave}};  // AND_Gate and_1, 2 bits wide
  assign and_2_out = \or  & not_1_out;  // AND_Gate and_2, 2 bits wide
  assign S = and_1_out | and_2_out;  // OR_Gate or_1, 2 bits wide
endmodule
