// Logisim project Exemplo0033.circ as structural Verilog: 2 circuits, main circuit main
module main (
  input  [1:0] a,
  input  [1:0] b,
  input  Chave,
  output [1:0] s1,
  output [1:0] s2
);

  wire [1:0] and_1_out, nand_1_out, nor_1_out, or_1_out;

  assign and_1_out = b & a;  // AND_Gate and_1, 2 bits wide
  assign nand_1_out = ~(b & a);  // NAND_Gate nand_1, 2 bits wide
  assign or_1_out = b | a;  // OR_Gate or_1, 2 bits wide
  assign nor_1_out = ~(b | a);  // NOR_Gate nor_1, 2 bits wide
  Multiplexador multiplexador_1 (.a(nand_1_out), .b(and_1_out), .chave(Chave), .S(s1));
  Multiplexador multiplexador_2 (.a(nor_1_out), .b(or_1_out), .chave(Chave), .S(s2));

  // Notes on the sheet:
  //   0 - Or / And 
  //                       1 - Nor / Nand
endmodule

module Multiplexador (
  input  [1:0] a,
  input  [1:0] b,
  input  chave,
  output [1:0] S
);

  wire [1:0] and_1_out, and_2_out, not_1_out;

  assign not_1_out = ~{2{chave}};  // NOT_Gate not_1, 2 bits wide
  assign and_1_out = a & {2{chave}};  // AND_Gate and_1, 2 bits wide
  assign and_2_out = b & not_1_out;  // AND_Gate and_2, 2 bits wide
  assign S = and_1_out | and_2_out;  // OR_Gate or_1, 2 bits wide
endmodule
