// Logisim project Exemplo0035.circ as structural Verilog: 2 circuits, main circuit main
module main (
  input  a,
  input  b,
  input  [2:0] Chave,
  output Saida
);

  wire and_1_out, nand_1_out, nor_1_out, not_1_out, not_2_out, or_1_out, undriven, xnor_1_out, xor_1_out;

  not not_1 (not_1_out, a);
  not not_2 (not_2_out, b);
  or or_1 (or_1_out, a, b);
  nor nor_1 (nor_1_out, a, b);
  and and_1 (and_1_out, a, b);
  nand nand_1 (nand_1_out, a, undriven, undriven, b);
  xor xor_1 (xor_1_out, a, b);
  xnor xnor_1 (xnor_1_out, a, b);
  Sel sel_1 (
    .a(not_1_out), .b(not_2_out), .c(or_1_out), .d(nor_1_out), .e(and_1_out), .f(nand_1_out), .g(xor_1_out),
    .h(xnor_1_out), .Chave(Chave), .Saida(Saida));

  // Notes on the sheet:
  //                                               100 - And
  //                                                               101 - Nand
  //                                         111 - Xnor
  //   000 - Not a
  //                      001 - Not b
  //             010 - Or
  //                              011 - Nor
  //                     110 - Xor
endmodule

module Sel (
  input  a,
  input  b,
  input  c,
  input  d,
  input  e,
  input  f,
  input  g,
  input  h,
  input  [2:0] Chave,
  output Saida
);

  wire and_1_out, and_2_out, and_3_out, and_4_out, and_5_out, and_6_out, and_7_out, and_8_out, not_1_out,
       not_2_out, not_3_out, not_4_out, not_5_out, not_6_out, not_7_out, not_8_out, not_9_out, not_10_out,
       not_11_out, not_12_out;

  not not_1 (not_1_out, Chave[2]);
  not not_2 (not_2_out, Chave[1]);
  not not_3 (not_3_out, Chave[0]);
  not not_4 (not_4_out, Chave[2]);
  not not_5 (not_5_out, Chave[1]);
  not not_6 (not_6_out, Chave[2]);
  not not_7 (not_7_out, Chave[0]);
  not not_8 (not_8_out, Chave[2]);
  not not_9 (not_9_out, Chave[1]);
  not not_10 (not_10_out, Chave[0]);
  not not_11 (not_11_out, Chave[1]);
  not not_12 (not_12_out, Chave[0]);
  and and_1 (and_1_out, a, not_1_out, not_2_out, not_3_out);
  and and_2 (and_2_out, b, not_4_out, not_5_out, Chave[0]);
  and and_3 (and_3_out, c, not_6_out, Chave[1], not_7_out);
  and and_4 (and_4_out, d, not_8_out, Chave[1], Chave[0]);
  and and_5 (and_5_out, e, Chave[2], not_9_out, not_10_out);
  and and_6 (and_6_out, f, Chave[2], not_11_out, Chave[0]);
  and and_7 (and_7_out, g, Chave[2], Chave[1], not_12_out);
  and and_8 (and_8_out, h, Chave[2], Chave[1], Chave[0]);
  or or_1 (Saida, and_1_out, and_2_out, and_3_out, and_4_out, and_5_out, and_6_out, and_7_out, and_8_out);
endmodule
