// Logisim project Exemplo0037.circ as structural Verilog: 2 circuits, main circuit main
module main (
  input  [3:0] a,
  input  [3:0] b,
  input  in_3,
  output [3:0] out_4
);

  wire [3:0] not_1_out, not_2_out, or_1_out, or_2_out;

  assign not_1_out = ~a;  // NOT_Gate not_1, 4 bits wide
  assign not_2_out = ~b;  // NOT_Gate not_2, 4 bits wide
  assign or_1_out = b | not_1_out;  // OR_Gate or_1, 4 bits wide
  assign or_2_out = not_2_out | a;  // OR_Gate or_2, 4 bits wide
  Multiplexador multiplexador_1 (.a(or_2_out), .b(or_1_out), .chave(in_3), .S(out_4));

  // Notes on the sheet:
  //                         1 - maior
  //   0 - menor
endmodule

module Multiplexador (
  input  [3:0] a,
  input  [3:0] b,
  input  chave,
  output [3:0] S
);

  wire [3:0] and_1_out, and_2_out, not_1_out;

  assign not_1_out = ~{4{chave}};  // NOT_Gate not_1, 4 bits wide
  assign and_1_out = a & {4{chave}};  // AND_Gate and_1, 4 bits wide
  assign and_2_out = b & not_1_out;  // AND_Gate and_2, 4 bits wide
  assign S = and_1_out | and_2_out;  // OR_Gate or_1, 4 bits wide
endmodule
