// Logisim project sim05.circ as structural Verilog: 1 circuit, main circuit main
module main (
  input  in_1,
  input  in_2,
  input  in_3,
  input  in_4,
  input  in_5,
  output out_6
);

  wire and_1_out, nand_1_out, nand_2_out, nand_3_out, nand_4_out, nand_5_out, nand_6_out, nand_7_out,
       nand_8_out, nand_9_out, nand_10_out, nand_11_out, nand_12_out, nand_13_out, nand_14_out, nand_15_out,
       nand_16_out, nand_17_out, nand_18_out, nand_19_out, nand_20_out, nand_21_out, nand_22_out,
       nand_23_out, nand_24_out, nand_25_out, nand_26_out, nand_27_out, nor_1_out, not_1_out, not_2_out,
       not_3_out, not_4_out, or_1_out, xnor_1_out, xor_1_out;

  and and_1 (and_1_out, in_4, in_5);
  nand nand_1 (nand_1_out, in_4, in_5);
  or or_1 (or_1_out, in_4, in_5);
  nor nor_1 (nor_1_out, in_4, in_5);
  xor xor_1 (xor_1_out, in_4, in_5);
  xnor xnor_1 (xnor_1_out, in_4, in_5);
  not not_1 (not_1_out, in_5);
  not not_2 (not_2_out, in_1);
  not not_3 (not_3_out, in_2);
  not not_4 (not_4_out, in_3);
  nand nand_2 (nand_2_out, not_4_out, not_3_out);
  nand nand_3 (nand_3_out, nand_2_out, nand_4_out);
  nand nand_4 (nand_4_out, and_1_out, not_2_out);
  nand nand_5 (nand_5_out, in_3, not_3_out);
  nand nand_6 (nand_6_out, nand_5_out, nand_7_out);
  nand nand_7 (nand_7_out, nand_1_out, not_2_out);
  nand nand_8 (nand_8_out, not_4_out, or_1_out);
  nand nand_9 (nand_9_out, nand_8_out, nand_10_out);
  nand nand_10 (nand_10_out, in_2, not_2_out);
  nand nand_11 (nand_11_out, in_3, nor_1_out);
  nand nand_12 (nand_12_out, nand_11_out, nand_13_out);
  nand nand_13 (nand_13_out, in_2, not_2_out);
  nand nand_14 (nand_14_out, xor_1_out, not_4_out);
  nand nand_15 (nand_15_out, nand_14_out, nand_16_out);
  nand nand_16 (nand_16_out, not_3_out, in_1);
  nand nand_17 (nand_17_out, xnor_1_out, in_3);
  nand nand_18 (nand_18_out, nand_17_out, nand_19_out);
  nand nand_19 (nand_19_out, not_3_out, in_1);
  nand nand_20 (nand_20_out, not_4_out, in_2);
  nand nand_21 (nand_21_out, nand_20_out, nand_22_out);
  nand nand_22 (nand_22_out, not_1_out, in_1);
  nand nand_23 (nand_23_out, nand_6_out, nand_3_out);
  nand nand_24 (nand_24_out, nand_12_out, nand_9_out);
  nand nand_25 (nand_25_out, nand_23_out, nand_24_out);
  nand nand_26 (nand_26_out, nand_18_out, nand_15_out);
  nand nand_27 (nand_27_out, nand_25_out, nand_26_out);
  nand nand_28 (out_6, nand_27_out, nand_21_out);
endmodule
