// Logisim project sim07.circ as structural Verilog: 1 circuit, main circuit main
module main (
  input  in_1,
  input  a1,
  input  a0,
  input  b1,
  input  b0,
  input  a,
  input  b,
  input  a_2,
  input  b_2,
  output out_10,
  output b___a,
  output a___b
);

  wire and_1_out, and_2_out, not_1_out, not_2_out, not_3_out, not_4_out, not_5_out, xor_1_out, xor_2_out,
       xor_3_out, xor_4_out;

  not not_1 (not_1_out, in_1);
  not not_2 (not_2_out, in_1);
  xor xor_1 (xor_1_out, in_1, a1);
  xor xor_2 (xor_2_out, b1, not_1_out);
  xor xor_3 (xor_3_out, in_1, a0);
  xor xor_4 (xor_4_out, b0, not_2_out);
  not not_3 (not_3_out, a);
  not not_4 (not_4_out, b_2);
  and and_1 (and_1_out, xor_1_out, xor_2_out);
  and and_2 (and_2_out, xor_3_out, xor_4_out);
  and and_3 (b___a, not_3_out, b);
  and and_4 (a___b, a_2, not_4_out);
  not not_5 (not_5_out, and_2_out);
  and and_5 (out_10, and_1_out, not_5_out);
endmodule
