// Logisim project Exemplo0033.circ as structural Verilog: 1 circuit, main circuit Ex3
module Ex3 (
  input  A,
  input  B,
  input  Chave,
  output [1:0] Saida
);

  wire and_1_out, nand_1_out, nor_1_out, not_1_out, not_2_out, or_1_out;
  wire [1:0] and_2_out, and_4_out;

  or or_1 (or_1_out, B, A);
  and and_1 (and_1_out, B, A);
  nand nand_1 (nand_1_out, B, A);
  nor nor_1 (nor_1_out, B, A);
  not not_1 (not_1_out, Chave);
  and and_2 (and_2_out[0], or_1_out, not_1_out);
  and and_3 (and_2_out[1], and_1_out, not_2_out);
  not not_2 (not_2_out, Chave);
  and and_4 (and_4_out[0], Chave, nor_1_out);
  and and_5 (and_4_out[1], Chave, nand_1_out);
  assign Saida = and_2_out | and_4_out;  // OR_Gate or_2, 2 bits wide
endmodule
