// Logisim project Exemplo0034.circ as structural Verilog: 1 circuit, main circuit Ex3
module Ex3 (
  input  A,
  input  B,
  input  ch_A,
  input  ch__B,
  output [1:0] Saida
);

  wire nor_1_out, not_1_out, not_2_out, not_3_out, not_4_out, or_1_out, xnor_1_out, xor_1_out;
  wire [1:0] and_1_out, and_3_out;

  or or_1 (or_1_out, B, A);
  nor nor_1 (nor_1_out, B, A);
  xor xor_1 (xor_1_out, B, A);
  xnor xnor_1 (xnor_1_out, B, A);
  not not_1 (not_1_out, ch_A);
  and and_1 (and_1_out[0], not_1_out, or_1_out, not_2_out);
  not not_2 (not_2_out, ch__B);
  not not_3 (not_3_out, ch_A);
  and and_2 (and_1_out[1], not_3_out, nor_1_out, ch__B);
  and and_3 (and_3_out[0], ch__B, xnor_1_out, ch_A);
  not not_4 (not_4_out, ch__B);
  and and_4 (and_3_out[1], not_4_out, xor_1_out, ch_A);
  assign Saida = and_1_out | and_3_out;  // OR_Gate or_2, 2 bits wide
endmodule
