// Logisim project Exemplo0035.circ as structural Verilog: 1 circuit, main circuit Ex3
module Ex3 (
  input  ch_A,
  input  ch_C,
  input  ch_C_2,
  input  A,
  input  B,
  output Saida
);

  wire and_1_out, and_2_out, and_3_out, and_4_out, and_5_out, and_6_out, and_7_out, and_8_out, nand_1_out,
       nor_1_out, not_1_out, not_2_out, not_3_out, not_4_out, not_5_out, not_6_out, not_7_out, not_8_out,
       not_9_out, not_10_out, not_11_out, not_12_out, not_13_out, or_1_out, xnor_1_out, xor_1_out;

  not not_1 (not_1_out, A);
  or or_1 (or_1_out, B, A);
  nor nor_1 (nor_1_out, B, A);
  and and_1 (and_1_out, B, A);
  nand nand_1 (nand_1_out, B, A);
  xor xor_1 (xor_1_out, B, A);
  xnor xnor_1 (xnor_1_out, B, A);
  not not_2 (not_2_out, ch_A);
  not not_3 (not_3_out, ch_C);
  not not_4 (not_4_out, ch_C_2);
  not not_5 (not_5_out, ch_A);
  not not_6 (not_6_out, ch_C);
  not not_7 (not_7_out, ch_A);
  not not_8 (not_8_out, ch_C_2);
  not not_9 (not_9_out, ch_A);
  not not_10 (not_10_out, ch_C);
  not not_11 (not_11_out, ch_C_2);
  not not_12 (not_12_out, ch_C);
  not not_13 (not_13_out, ch_C_2);
  and and_2 (and_2_out, not_2_out, not_4_out, not_1_out);
  and and_3 (and_3_out, not_5_out, ch_C_2, or_1_out);
  and and_4 (and_4_out, not_7_out, not_8_out, nor_1_out);
  and and_5 (and_5_out, not_9_out, ch_C_2, and_1_out);
  and and_6 (and_6_out, ch_A, not_11_out, nand_1_out);
  and and_7 (and_7_out, ch_A, ch_C_2, xor_1_out);
  and and_8 (and_8_out, ch_A, not_13_out, xnor_1_out);
  or or_2 (Saida, and_2_out, and_3_out, and_4_out, and_5_out, and_6_out, and_7_out, and_8_out);
endmodule
