// Logisim project Exemplo0032.circ as structural Verilog: 1 circuit, main circuit main
module main (
  input  [1:0] b,
  input  [1:0] a,
  input  in_3,
  output [1:0] out_4
);

  wire [1:0] and_1_out, and_2_out, and_3_out, not_1_out, or_1_out;

  assign and_1_out = a & b;  // AND_Gate and_1, 2 bits wide
  assign or_1_out = b | a;  // OR_Gate or_1, 2 bits wide
  assign and_2_out = and_1_out & {2{in_3}};  // AND_Gate and_2, 2 bits wide
  assign and_3_out = or_1_out & not_1_out;  // AND_Gate and_3, 2 bits wide
  assign not_1_out = ~{2{in_3}};  // NOT_Gate not_1, 2 bits wide
  assign out_4 = and_2_out | and_3_out;  // OR_Gate or_2, 2 bits wide
endmodule
