// Logisim project Exemplo0035_logisim.circ as structural Verilog: 2 circuits, main circuit main
module main (
  input  a,
  input  b,
  input  chave0,
  input  chave1,
  input  chave2,
  output s
);

  subcircuito subcircuito_1 (.a(a), .b(b), .chave0(chave0), .chave1(chave1), .chave2(chave2), .s(s));
endmodule

module subcircuito (
  input  a,
  input  b,
  input  chave0,
  input  chave1,
  input  chave2,
  output s
);

  wire and_1_out, and_2_out, and_3_out, and_4_out, and_5_out, and_6_out, and_7_out, and_8_out, and_9_out,
       nand_1_out, nor_1_out, not_1_out, not_2_out, not_3_out, not_4_out, not_5_out, not_6_out, not_7_out,
       not_8_out, not_9_out, not_10_out, not_11_out, not_12_out, not_13_out, not_14_out, or_1_out, or_2_out,
       or_3_out, or_4_out, or_5_out, or_6_out, or_7_out, xnor_1_out, xor_1_out;

  not not_1 (not_1_out, a);
  not not_2 (not_2_out, b);
  or or_1 (or_1_out, a, b);
  nor nor_1 (nor_1_out, a, b);
  and and_1 (and_1_out, a, b);
  nand nand_1 (nand_1_out, a, b);
  xor xor_1 (xor_1_out, a, b);
  xnor xnor_1 (xnor_1_out, a, b);
  not not_3 (not_3_out, chave0);
  not not_4 (not_4_out, chave1);
  not not_5 (not_5_out, chave2);
  not not_6 (not_6_out, chave0);
  not not_7 (not_7_out, chave1);
  not not_8 (not_8_out, chave0);
  not not_9 (not_9_out, chave2);
  not not_10 (not_10_out, chave0);
  not not_11 (not_11_out, chave1);
  not not_12 (not_12_out, chave2);
  not not_13 (not_13_out, chave1);
  not not_14 (not_14_out, chave2);
  and and_2 (and_2_out, not_1_out, not_3_out, not_4_out, not_5_out);
  and and_3 (and_3_out, not_2_out, not_6_out, not_7_out, chave2);
  and and_4 (and_4_out, or_1_out, not_8_out, chave1, not_9_out);
  and and_5 (and_5_out, nor_1_out, not_10_out, chave1, chave2);
  and and_6 (and_6_out, and_1_out, chave0, not_11_out, not_12_out);
  and and_7 (and_7_out, nand_1_out, chave0, not_13_out, chave2);
  and and_8 (and_8_out, xor_1_out, chave0, chave1, not_14_out);
  and and_9 (and_9_out, xnor_1_out, chave0, chave1, chave2);
  or or_2 (or_2_out, and_2_out, and_3_out);
  or or_3 (or_3_out, and_4_out, and_5_out);
  or or_4 (or_4_out, and_6_out, and_7_out);
  or or_5 (or_5_out, and_8_out, and_9_out);
  or or_6 (or_6_out, or_2_out, or_3_out);
  or or_7 (or_7_out, or_4_out, or_5_out);
  or or_8 (s, or_6_out, or_7_out);
endmodule
