// Logisim project Exemplo0034.circ as structural Verilog: 1 circuit, main circuit main
module main (
  input  A,
  input  B,
  input  in_3,
  input  in_4,
  output out_5,
  output out_6,
  output out_7,
  output out_8
);

  wire nor_1_out, not_1_out, not_2_out, not_3_out, not_4_out, or_1_out, xnor_1_out, xor_1_out;

  xor xor_1 (xor_1_out, B, A);
  xnor xnor_1 (xnor_1_out, B, A);
  nor nor_1 (nor_1_out, B, A);
  or or_1 (or_1_out, B, A);
  not not_1 (not_1_out, in_4);
  not not_2 (not_2_out, in_3);
  not not_3 (not_3_out, in_4);
  not not_4 (not_4_out, in_3);
  and and_1 (out_5, xor_1_out, in_3);
  and and_2 (out_6, xnor_1_out, in_4);
  and and_3 (out_7, not_2_out, or_1_out);
  and and_4 (out_8, not_4_out, nor_1_out);
endmodule
