// Logisim project Exemplo0034.circ as structural Verilog: 2 circuits, main circuit main
module chave (
  input  [1:0] a,
  input  [1:0] b,
  input  [1:0] Seletor,
  output [1:0] out_4
);

  wire [1:0] and_1_out, and_2_out, and_3_out, and_4_out, and_5_out, and_6_out, not_1_out, not_2_out,
       or_1_out, or_2_out, or_3_out, xor_1_out;
  wire [1:1] not_3_out, not_4_out;

  assign or_1_out = a | b;  // OR_Gate or_1, 2 bits wide
  assign not_1_out = ~or_1_out;  // NOT_Gate not_1, 2 bits wide
  assign xor_1_out = a ^ b;  // XOR_Gate xor_1, 2 bits wide
  assign not_2_out = ~xor_1_out;  // NOT_Gate not_2, 2 bits wide
  not not_3 (not_3_out[1], Seletor[1]);
  not not_4 (not_4_out[1], Seletor[0]);
  assign and_1_out = or_1_out & {2{not_4_out[1]}};  // AND_Gate and_1, 2 bits wide
  assign or_2_out = and_1_out | and_2_out;  // OR_Gate or_2, 2 bits wide
  assign and_2_out = not_1_out & {2{Seletor[0]}};  // AND_Gate and_2, 2 bits wide
  assign and_3_out = xor_1_out & {2{not_4_out[1]}};  // AND_Gate and_3, 2 bits wide
  assign and_4_out = not_2_out & {2{Seletor[0]}};  // AND_Gate and_4, 2 bits wide
  assign and_5_out = {2{not_3_out[1]}} & or_2_out;  // AND_Gate and_5, 2 bits wide
  assign or_3_out = and_3_out | and_4_out;  // OR_Gate or_3, 2 bits wide
  assign and_6_out = or_3_out & {2{Seletor[1]}};  // AND_Gate and_6, 2 bits wide
  assign out_4 = and_5_out | and_6_out;  // OR_Gate or_4, 2 bits wide

  // Notes on the sheet:
  //   s0
  //   s1
  //   s2
  //   s3
endmodule

module main (
  input  [1:0] a,
  input  [1:0] b,
  input  [1:0] seletor,
  output [1:0] out_4
);

  chave chave_1 (.out_4(out_4), .a(a), .b(b), .Seletor(seletor));

  // Notes on the sheet:
  //   0 - or
  //   1 - nor
  //   Seleção de operações
  //   2 - xor
  //   3 - xnor
endmodule
