// Logisim project Exemplo0036.circ as structural Verilog: 1 circuit, main circuit main
module main (
  input  [3:0] a,
  input  [3:0] b,
  output _0____igual____1____diferente
);

  wire [3:0] xnor_1_out;

  assign xnor_1_out = ~(b ^ a);  // XNOR_Gate xnor_1, 4 bits wide
  nand nand_1 (_0____igual____1____diferente, xnor_1_out[0], xnor_1_out[1], xnor_1_out[2], xnor_1_out[3]);
endmodule
