// Logisim project Exemplo0031.circ as structural Verilog: 1 circuit, main circuit main
module main (
  input  a1,
  input  b1,
  input  c1,
  input  d1,
  input  a2,
  input  b2,
  input  c2,
  input  d2,
  output out_9,
  output out_10,
  output out_11,
  output out_12,
  output out_13,
  output out_14,
  output out_15,
  output out_16
);

  and and_1 (out_12, d1, d2);
  or or_1 (out_16, d1, d2);
  and and_2 (out_11, c1, c2);
  or or_2 (out_15, c1, c2);
  and and_3 (out_10, b1, b2);
  or or_3 (out_14, b1, b2);
  and and_4 (out_9, a1, a2);
  or or_4 (out_13, a1, a2);

  // Notes on the sheet:
  //   saida AND
  //   Saida OR
endmodule
