// Logisim project Exemplo0032.circ as structural Verilog: 1 circuit, main circuit main
module main (
  input  a,
  input  b,
  input  c,
  input  d,
  input  SW,
  output ac,
  output bd
);

  wire A1_out, A2_out, A3_out, A4_out, AAC_out, ABD_out, N1_out, N2_out, OAC_out, OBD_out;

  and AAC (AAC_out, c, a);
  or OAC (OAC_out, c, a);
  and ABD (ABD_out, d, b);
  or OBD (OBD_out, d, b);
  not N1 (N1_out, SW);
  not N2 (N2_out, SW);
  and A1 (A1_out, AAC_out, SW);
  and A2 (A2_out, OAC_out, N1_out);
  and A3 (A3_out, ABD_out, SW);
  and A4 (A4_out, OBD_out, N2_out);
  or O1 (ac, A1_out, A2_out);
  or O2 (bd, A3_out, A4_out);

  // Notes on the sheet:
  //   saac
  //   soac
  //   sabd
  //   sobd
  //   SW
  //   SW
  //   saac
  //   s0
  //   SW
  //   soac
  //   s1
  //   n0
  //   sabd
  //   s2
  //   SW
  //   sobd
  //   s3
  //   n1
  //   ac
  //   bd
endmodule
