// Logisim project Exemplo0032_alternativo.circ as structural Verilog: 3 circuits, main circuit main
module main (
  input  a,
  input  b,
  input  c,
  input  d,
  input  Switch,
  output s0,
  output s1
);

  wire AND_ac_out, AND_bd_out, OR_ac_out, OR_bd_out;

  and AND_ac (AND_ac_out, a, c);
  or OR_ac (OR_ac_out, a, c);
  and AND_bd (AND_bd_out, b, d);
  or OR_bd (OR_bd_out, b, d);
  Switch4bits switch4bits_1 (
    .e0(AND_ac_out), .e1(OR_ac_out), .e2(AND_bd_out), .e3(OR_bd_out), .Switch(Switch), .s0(s0), .s1(s1));

  // Notes on the sheet:
  //   a
  //   saac
  //   c
  //   a
  //   soac
  //   c
  //   b
  //   sabd
  //   d
  //   b
  //   sobd
  //   d
endmodule

// Sw02
module Switch2bits (
  input  e0,
  input  e1,
  input  Switch,
  output s
);

  wire Livre_out, Negado_out, Not00_out;

  not Not00 (Not00_out, Switch);
  and Livre (Livre_out, e0, Switch);
  and Negado (Negado_out, e1, Not00_out);
  or Or00 (s, Livre_out, Negado_out);

  // Notes on the sheet:
  //   n0
  //   s0
  //   s1
endmodule

// 4bits
module Switch4bits (
  input  e0,
  input  e1,
  input  e2,
  input  e3,
  input  Switch,
  output s0,
  output s1
);

  Switch2bits switch2bits_1 (.e0(e0), .e1(e1), .Switch(Switch), .s(s0));
  Switch2bits switch2bits_2 (.e0(e2), .e1(e3), .Switch(Switch), .s(s1));
endmodule
