// Logisim project Exemplo0033.circ as structural Verilog: 1 circuit, main circuit main
module main (
  input  a,
  input  b,
  input  c,
  input  d,
  input  SW,
  output OR_NOR,
  output out_7,
  output AND_NAND,
  output out_9
);

  wire A1_out, A2_out, A3_out, A4_out, A5_out, A6_out, A7_out, A8_out, A9_out, A10_out, N1_out, N2_out,
       N3_out, N4_out, NA1_out, NA2_out, NO1_out, NO2_out, O1_out, O2_out;

  or O1 (O1_out, a, c);
  nor NO1 (NO1_out, a, c);
  or O2 (O2_out, b, d);
  nor NO2 (NO2_out, b, d);
  and A1 (A1_out, a, c);
  nand NA1 (NA1_out, a, c);
  and A2 (A2_out, b, d);
  nand NA2 (NA2_out, b, d);
  not N1 (N1_out, SW);
  not N2 (N2_out, SW);
  not N3 (N3_out, SW);
  not N4 (N4_out, SW);
  and A3 (A3_out, O1_out, N1_out);
  and A4 (A4_out, NO1_out, SW);
  and A5 (A5_out, O2_out, N2_out);
  and A6 (A6_out, NO2_out, SW);
  and A7 (A7_out, A1_out, N3_out);
  and A8 (A8_out, NA1_out, SW);
  and A9 (A9_out, A2_out, N4_out);
  and A10 (A10_out, NA2_out, SW);
  or O3 (OR_NOR, A3_out, A4_out);
  or O4 (out_7, A5_out, A6_out);
  or O5 (AND_NAND, A7_out, A8_out);
  or O6 (out_9, A9_out, A10_out);

  // Notes on the sheet:
  //   a
  //   c
  //   a
  //   c
  //   b
  //   d
  //   b
  //   d
  //   a
  //   c
  //   a
  //   c
  //   b
  //   d
  //   b
  //   d
  //   so1ac
  //   sno1ac
  //   so2bd
  //   sno2bd
  //   sa1ac
  //   sna1ac
  //   sa2bd
  //   sna2bd
  //   SW
  //   SW
  //   SW
  //   SW
  //   n1
  //   SW
  //   n2
  //   SW
  //   n3
  //   SW
  //   n4
  //   SW
  //   s0
  //   Oac
  //   s1
  //   s2
  //   Obd
  //   s3
  //   s4
  //   Nac
  //   s5
  //   s6
  //   Nbd
  //   s7
endmodule
