// Logisim project Exemplo0034.circ as structural Verilog: 1 circuit, main circuit main
module main (
  input  a,
  input  b,
  input  c,
  input  d,
  input  C1,
  input  C2,
  output ac,
  output bd
);

  wire A1_out, A2_out, A3_out, A4_out, A5_out, A6_out, A7_out, A8_out, N1_out, N2_out, N3_out, N4_out,
       N5_out, N6_out, N7_out, N8_out, NO1_out, NO2_out, O1_out, O2_out, X1_out, X2_out, XO1_out, XO2_out;

  or O1 (O1_out, a, c);
  nor NO1 (NO1_out, a, c);
  xor X1 (X1_out, a, c);
  xnor XO1 (XO1_out, a, c);
  or O2 (O2_out, b, d);
  nor NO2 (NO2_out, b, d);
  xor X2 (X2_out, b, d);
  xnor XO2 (XO2_out, b, d);
  not N1 (N1_out, C1);
  not N2 (N2_out, C2);
  not N3 (N3_out, C1);
  not N4 (N4_out, C2);
  not N5 (N5_out, C1);
  not N6 (N6_out, C2);
  not N7 (N7_out, C1);
  not N8 (N8_out, C2);
  and A1 (A1_out, O1_out, N1_out, N2_out);
  and A2 (A2_out, NO1_out, N3_out, C2);
  and A3 (A3_out, X1_out, C1, N4_out);
  and A4 (A4_out, XO1_out, C1, C2);
  and A5 (A5_out, O2_out, N5_out, N6_out);
  and A6 (A6_out, NO2_out, N7_out, C2);
  and A7 (A7_out, X2_out, C1, N8_out);
  and A8 (A8_out, XO2_out, C1, C2);
  or OR1 (ac, A1_out, A2_out, A3_out, A4_out);
  or OR2 (bd, A5_out, A6_out, A7_out, A8_out);

  // Notes on the sheet:
  //   a
  //   o1
  //   c
  //   a
  //   no1
  //   c
  //   a
  //   x1
  //   c
  //   a
  //   c
  //   b
  //   o2
  //   d
  //   b
  //   no2
  //   d
  //   b
  //   x2
  //   d
  //   b
  //   d
  //   xo1
  //   xo2
  //   c1
  //   c2
  //   c1
  //   c2
  //   c1
  //   c2
  //   c1
  //   c2
  //   o1
  //   n1
  //   n2
  //   no1
  //   n3
  //   c2
  //   x1
  //   c1
  //   n4
  //   xo1
  //   c1
  //   c2
  //   o2
  //   n5
  //   n6
  //   no2
  //   n7
  //   c2
  //   x2
  //   c1
  //   n8
  //   xo2
  //   c1
  //   c2
  //   s0
  //   s1
  //   s2
  //   s3
  //   s4
  //   s5
  //   s6
  //   s7
  //   ac
  //   bd
endmodule
