// Logisim project Exemplo0035.circ as structural Verilog: 1 circuit, main circuit main
module main (
  input  a,
  input  b,
  input  c,
  input  c1,
  input  c2,
  input  c3,
  output S
);

  wire A0_out, A1_out, A2_out, A3_out, A4_out, A5_out, A6_out, E0_out, E1_out, E2_out, E3_out, E4_out,
       E5_out, E6_out, N1_out, N2_out, N3_out, N4_out, N5_out, N6_out, N7_out, N8_out, N9_out, N10_out,
       N11_out, N12_out;

  not E0 (E0_out, c);
  or E1 (E1_out, b, a);
  nor E2 (E2_out, b, a);
  and E3 (E3_out, b, a);
  nand E4 (E4_out, b, a);
  xor E5 (E5_out, b, a);
  xnor E6 (E6_out, b, a);
  not N1 (N1_out, c1);
  not N2 (N2_out, c2);
  not N3 (N3_out, c3);
  not N4 (N4_out, c1);
  not N5 (N5_out, c2);
  not N6 (N6_out, c1);
  not N7 (N7_out, c3);
  not N8 (N8_out, c1);
  not N9 (N9_out, c2);
  not N10 (N10_out, c3);
  not N11 (N11_out, c2);
  not N12 (N12_out, c3);
  and A0 (A0_out, E0_out, N1_out, N2_out, N3_out);
  and A1 (A1_out, E1_out, N4_out, N5_out, c3);
  and A2 (A2_out, E2_out, N6_out, c2, N7_out);
  and A3 (A3_out, E3_out, N8_out, c2, c3);
  and A4 (A4_out, E4_out, c1, N9_out, N10_out);
  and A5 (A5_out, E5_out, c1, N11_out, c3);
  and A6 (A6_out, E6_out, c1, c2, N12_out);
  or O1 (S, A0_out, A1_out, A2_out, A3_out, A4_out, A5_out, A6_out);

  // Notes on the sheet:
  //   e0
  //   e1
  //   e2
  //   e3
  //   e4
  //   e5
  //   e6
  //   c1
  //   c2
  //   c3
  //   c1
  //   c2
  //   c1
  //   c3
  //   c1
  //   c2
  //   c3
  //   c2
  //   c3
  //   e0
  //   n1
  //   n2
  //   n3
  //   e1
  //   n4
  //   n5
  //   c3
  //   e2
  //   n6
  //   c2
  //   n7
  //   e3
  //   n8
  //   c2
  //   c3
  //   e4
  //   c1
  //   n9
  //   n10
  //   e5
  //   c1
  //   n11
  //   c3
  //   e6
  //   c1
  //   c2
  //   n12
  //   s0
  //   s1
  //   s2
  //   s3
  //   s4
  //   s5
  //   s6
  //   S
endmodule
