// Logisim project CIRC01.circ as structural Verilog: 1 circuit, main circuit CIRC01
module CIRC01 (
  input  a,
  input  b,
  input  e,
  input  f,
  input  c,
  input  d,
  input  g,
  input  h,
  output aeOR,
  output bfOR,
  output aeAND,
  output bfAND,
  output cgOR,
  output dhOR,
  output cgAND,
  output dhAND
);

  or or_1 (cgOR, c, g);
  and and_1 (cgAND, c, g);
  or or_2 (aeOR, a, e);
  and and_2 (aeAND, a, e);
  or or_3 (bfOR, b, f);
  and and_3 (bfAND, b, f);
  or or_4 (dhOR, d, h);
  and and_4 (dhAND, d, h);
endmodule
