// Logisim project CIRC02.circ as structural Verilog: 1 circuit, main circuit CIRC02
module CIRC02 (
  input  a,
  input  b,
  input  c,
  input  d,
  input  ch,
  output ac,
  output bd
);

  wire ANDac_out, ANDbd_out, ANDs0_out, ANDs1_out, ANDs2_out, ANDs3_out, not_1_out, not_2_out, ORac_out,
       ORbd_out;

  and ANDac (ANDac_out, c, a);
  or ORac (ORac_out, a, c);
  and ANDbd (ANDbd_out, d, b);
  or ORbd (ORbd_out, d, b);
  not not_1 (not_1_out, ch);
  not not_2 (not_2_out, ch);
  and ANDs0 (ANDs0_out, ANDac_out, ch);
  and ANDs1 (ANDs1_out, not_1_out, ORac_out);
  and ANDs2 (ANDs2_out, ANDbd_out, ch);
  and ANDs3 (ANDs3_out, ORbd_out, not_2_out);
  or s0s1 (ac, ANDs0_out, ANDs1_out);
  or s2s3 (bd, ANDs2_out, ANDs3_out);
endmodule
