// Logisim project CIRC03.circ as structural Verilog: 1 circuit, main circuit main
module main (
  input  a,
  input  b,
  input  CH,
  output s0,
  output s1
);

  wire AND01_out, AND02_out, AND03_out, AND04_out, ANDab_out, NANDab_out, NORab_out, not_1_out, not_2_out,
       ORab_out;

  and ANDab (ANDab_out, a, b);
  or ORab (ORab_out, a, b);
  nand NANDab (NANDab_out, a, b);
  nor NORab (NORab_out, a, b);
  not not_1 (not_1_out, CH);
  not not_2 (not_2_out, CH);
  and AND01 (AND01_out, ANDab_out, not_1_out);
  and AND02 (AND02_out, NANDab_out, CH);
  and AND03 (AND03_out, ORab_out, not_2_out);
  and AND04 (AND04_out, NORab_out, CH);
  or OR01 (s0, AND01_out, AND02_out);
  or OR02 (s1, AND03_out, AND04_out);
endmodule
