// Logisim project Exemplo0031.circ as structural Verilog
module Exericio01 (
  input  a,
  input  b,
  input  c,
  input  d,
  output out_5,
  output out_6
);

  and AND (out_5, a, b, c, d);
  or OR (out_6, a, b, c, d);
endmodule
