// Logisim project Exemplo0032.circ as structural Verilog: 2 circuits, main circuit SEL
module SEL (
  input  x,
  input  y,
  input  chave,
  output out_4
);

  wire and_1_out, and_2_out, not_1_out;

  not not_1 (not_1_out, chave);
  and and_1 (and_1_out, y, chave);
  and and_2 (and_2_out, x, not_1_out);
  or or_1 (out_4, and_1_out, and_2_out);
endmodule

module Exercicio2 (
  input  a,
  input  b,
  input  Chave,
  output out_4
);

  wire AND_out, OR_out;

  and AND (AND_out, b, a);
  or OR (OR_out, b, a);
  SEL sel_1 (.x(OR_out), .y(AND_out), .chave(Chave), .out_4(out_4));

  // Notes on the sheet:
  //   1 - AND
  //   0 - OR
endmodule
