// Logisim project Exemplo0033.circ as structural Verilog: 2 circuits, main circuit SEL
module SEL (
  input  a,
  input  b,
  input  c,
  input  d,
  input  chave,
  output s1,
  output s2
);

  wire AND1_out, AND2_out, AND3_out, AND4_out, not_1_out, not_2_out;

  not not_1 (not_1_out, chave);
  not not_2 (not_2_out, chave);
  and AND1 (AND1_out, a, not_1_out);
  and AND2 (AND2_out, b, not_2_out);
  and AND3 (AND3_out, c, chave);
  and AND4 (AND4_out, d, chave);
  or OR1 (s1, AND1_out, AND2_out);
  or OR2 (s2, AND3_out, AND4_out);
endmodule

module Exemplo0033 (
  input  x,
  input  y,
  input  chave,
  output s1,
  output s2
);

  wire AND_out, NAND_out, NOR_out, OR_out;

  and AND (AND_out, y, x);
  or OR (OR_out, y, x);
  nand NAND (NAND_out, y, x);
  nor NOR (NOR_out, y, x);
  SEL sel_1 (.a(AND_out), .b(OR_out), .c(NAND_out), .d(NOR_out), .chave(chave), .s1(s1), .s2(s2));
endmodule
