// Logisim project Exemplo0034.circ as structural Verilog: 2 circuits, main circuit SEL
module SEL (
  input  a,
  input  b,
  input  c,
  input  d,
  input  [1:0] chave,
  output s1
);

  wire AND1_out, AND2_out, AND3_out, AND4_out, not_1_out, not_2_out, not_3_out, not_4_out;

  not not_1 (not_1_out, chave[1]);
  not not_2 (not_2_out, chave[0]);
  not not_3 (not_3_out, chave[0]);
  not not_4 (not_4_out, chave[1]);
  and AND1 (AND1_out, a, not_1_out, not_2_out);
  and AND2 (AND2_out, b, chave[1], not_3_out);
  and AND3 (AND3_out, c, not_4_out, chave[0]);
  and AND4 (AND4_out, d, chave[1], chave[0]);
  or OR1 (s1, AND1_out, AND2_out, AND3_out, AND4_out);

  // Notes on the sheet:
  //   p1
  //   p2
  //   p3
  //   p4
endmodule

module Exemplo0034 (
  input  x,
  input  y,
  input  [1:0] chave,
  output s
);

  wire OR_2_out, OR_out, XNOR_out, XOR_out;

  or OR (OR_out, y, x);
  nor OR_2 (OR_2_out, y, x);
  xor XOR (XOR_out, y, x);
  xnor XNOR (XNOR_out, y, x);
  SEL sel_1 (.a(OR_out), .b(OR_2_out), .c(XOR_out), .d(XNOR_out), .chave(chave), .s1(s));
endmodule
