// Logisim project Exemplo0035.circ as structural Verilog: 2 circuits, main circuit SEL
module SEL (
  input  a,
  input  b,
  input  c,
  input  d,
  input  e,
  input  f,
  input  g,
  input  h,
  input  [2:0] chave,
  output s0
);

  wire AND1_out, AND2_out, AND3_out, AND4_out, AND5_out, AND6_out, AND7_out, AND8_out, not_1_out, not_2_out,
       not_3_out, not_4_out, not_5_out, not_6_out, not_7_out, not_8_out, not_9_out, not_10_out, not_11_out,
       not_12_out;

  not not_1 (not_1_out, chave[2]);
  not not_2 (not_2_out, chave[1]);
  not not_3 (not_3_out, chave[0]);
  not not_4 (not_4_out, chave[2]);
  not not_5 (not_5_out, chave[1]);
  not not_6 (not_6_out, chave[2]);
  not not_7 (not_7_out, chave[0]);
  not not_8 (not_8_out, chave[2]);
  not not_9 (not_9_out, chave[1]);
  not not_10 (not_10_out, chave[0]);
  not not_11 (not_11_out, chave[1]);
  not not_12 (not_12_out, chave[0]);
  and AND1 (AND1_out, a, not_1_out, not_2_out, not_3_out);
  and AND2 (AND2_out, b, not_4_out, not_5_out, chave[0]);
  and AND3 (AND3_out, c, not_6_out, chave[1], not_7_out);
  and AND4 (AND4_out, d, not_8_out, chave[1], chave[0]);
  and AND5 (AND5_out, e, chave[2], not_9_out, not_10_out);
  and AND6 (AND6_out, f, chave[2], not_11_out, chave[0]);
  and AND7 (AND7_out, g, chave[2], chave[1], not_12_out);
  and AND8 (AND8_out, h, chave[2], chave[1], chave[0]);
  or OR (s0, AND1_out, AND2_out, AND3_out, AND4_out, AND5_out, AND6_out, AND7_out, AND8_out);
endmodule

module Exemplo0035 (
  input  x,
  input  y,
  input  [2:0] chave,
  output s
);

  wire AND_out, NAND_out, NOR_out, not_1_out, NOT_Y_out, OR_out, XNOR_out, XOR_out;

  not NOT_Y (NOT_Y_out, y);
  not not_1 (not_1_out, x);
  and AND (AND_out, y, x);
  or OR (OR_out, y, x);
  nand NAND (NAND_out, y, x);
  nor NOR (NOR_out, y, x);
  xor XOR (XOR_out, y, x);
  xnor XNOR (XNOR_out, y, x);
  SEL sel_1 (
    .a(NOT_Y_out), .b(not_1_out), .c(AND_out), .d(OR_out), .e(NAND_out), .f(NOR_out), .g(XOR_out),
    .h(XNOR_out), .chave(chave), .s0(s));

  // Notes on the sheet:
  //   NOT X
endmodule
