// Logisim project Guia03.circ as structural Verilog: 5 circuits, main circuit Ex1
module Ex1 (
  input  [3:0] in_1,
  input  [3:0] in_2,
  output [3:0] out_3,
  output [3:0] out_4
);

  assign out_3 = in_1 & in_2;  // AND_Gate and_1, 4 bits wide
  assign out_4 = in_1 | in_2;  // OR_Gate or_1, 4 bits wide

  // Notes on the sheet:
  //   Miller - 449048
  //   Arquitetura de Computadores - Theldo
  //   Portas AND e OR simultaneas
endmodule

module Ex2 (
  input  [1:0] in_1,
  input  [1:0] in_2,
  input  in_3,
  output [1:0] out_4
);

  wire [1:0] and_1_out, and_2_out, and_3_out, not_1_out, or_1_out;

  assign or_1_out = in_1 | in_2;  // OR_Gate or_1, 2 bits wide
  assign and_1_out = in_1 & in_2;  // AND_Gate and_1, 2 bits wide
  assign and_2_out = or_1_out & not_1_out;  // AND_Gate and_2, 2 bits wide
  assign not_1_out = ~{2{in_3}};  // NOT_Gate not_1, 2 bits wide
  assign and_3_out = {2{in_3}} & and_1_out;  // AND_Gate and_3, 2 bits wide
  assign out_4 = and_2_out | and_3_out;  // OR_Gate or_2, 2 bits wide

  // Notes on the sheet:
  //   Miller - 449048
  //   AND e OR selecionavel
  //   Arquitetura de Computadores
endmodule

module Ex3 (
  input  Selecionar_Grupo,
  input  [1:0] in_2,
  input  [1:0] in_3,
  output [1:0] out_4,
  output [1:0] out_5,
  output [1:0] out_6,
  output [1:0] out_7
);

  wire [1:0] and_3_out, nand_1_out, nor_1_out, not_1_out, or_1_out;

  assign nand_1_out = ~(in_2 & in_3);  // NAND_Gate nand_1, 2 bits wide
  assign nor_1_out = ~(in_2 | in_3);  // NOR_Gate nor_1, 2 bits wide
  assign not_1_out = ~{2{Selecionar_Grupo}};  // NOT_Gate not_1, 2 bits wide
  assign out_4 = nand_1_out & {2{Selecionar_Grupo}};  // AND_Gate and_1, 2 bits wide
  assign out_5 = {2{Selecionar_Grupo}} & nor_1_out;  // AND_Gate and_2, 2 bits wide
  assign and_3_out = in_2 & in_3;  // AND_Gate and_3, 2 bits wide
  assign or_1_out = in_2 | in_3;  // OR_Gate or_1, 2 bits wide
  assign out_6 = and_3_out & not_1_out;  // AND_Gate and_4, 2 bits wide
  assign out_7 = not_1_out & or_1_out;  // AND_Gate and_5, 2 bits wide

  // Notes on the sheet:
  //   Valores de Entrada
  //   0 = AND/OR
  //   1 = NAND/NOR
  //   Grupo NAND / NOR
  //   Grupo AND / OR
endmodule

module Ex4 (
  input  [1:0] Chave,
  input  [1:0] Entrada_A,
  input  [1:0] Entrada_B,
  output [1:0] Saida_S
);

  wire [1:0] and_1_out, and_2_out, and_3_out, and_4_out, nor_1_out, not_4_out, or_1_out, xnor_1_out,
       xor_1_out;
  wire [1:1] not_1_out, not_2_out, not_3_out;

  not not_1 (not_1_out[1], Chave[1]);
  not not_2 (not_2_out[1], Chave[0]);
  not not_3 (not_3_out[1], Chave[0]);
  assign or_1_out = Entrada_A | Entrada_B;  // OR_Gate or_1, 2 bits wide
  assign nor_1_out = ~(Entrada_A | Entrada_B);  // NOR_Gate nor_1, 2 bits wide
  assign and_1_out = {2{not_1_out[1]}} & {2{not_2_out[1]}} & or_1_out;  // AND_Gate and_1, 2 bits wide
  assign and_2_out = nor_1_out & {2{not_1_out[1]}} & {2{Chave[0]}};  // AND_Gate and_2, 2 bits wide
  assign xor_1_out = Entrada_A ^ Entrada_B;  // XOR_Gate xor_1, 2 bits wide
  assign xnor_1_out = ~(Entrada_B ^ Entrada_A);  // XNOR_Gate xnor_1, 2 bits wide
  assign and_3_out = {2{Chave[1]}} & {2{not_3_out[1]}} & xor_1_out;  // AND_Gate and_3, 2 bits wide
  assign and_4_out = {2{Chave[1]}} & not_4_out & xnor_1_out;  // AND_Gate and_4, 2 bits wide
  assign not_4_out = ~{2{not_3_out[1]}};  // NOT_Gate not_4, 2 bits wide
  assign Saida_S = and_1_out | and_2_out | and_3_out | and_4_out;  // OR_Gate or_2, 2 bits wide
endmodule

module Ex5 (
  input  [2:0] Chave,
  input  [2:0] Entrada_A,
  input  [2:0] Entrada_B,
  output [2:0] Saida_S
);

  wire [2:0] _000_out, _001_out, _010_out, _011_out, _100_out, _101_out, and_1_out, and_2_out, and_3_out,
       and_4_out, and_5_out, and_6_out;
  wire [2:2] not_1_out, not_2_out, not_3_out, not_4_out, not_5_out, not_6_out, not_7_out, not_8_out,
       not_9_out, not_10_out, not_11_out;

  not not_1 (not_1_out[2], Chave[1]);
  not not_2 (not_2_out[2], Chave[1]);
  not not_3 (not_3_out[2], Chave[1]);
  not not_4 (not_4_out[2], Chave[2]);
  not not_5 (not_5_out[2], Chave[2]);
  not not_6 (not_6_out[2], Chave[0]);
  not not_7 (not_7_out[2], Chave[2]);
  not not_8 (not_8_out[2], Chave[1]);
  not not_9 (not_9_out[2], Chave[0]);
  not not_10 (not_10_out[2], Chave[0]);
  not not_11 (not_11_out[2], Chave[2]);
  assign _000_out = Entrada_B | Entrada_A;  // OR_Gate _000, 3 bits wide
  assign _001_out = ~(Entrada_A | Entrada_B);  // NOR_Gate _001, 3 bits wide
  assign _010_out = Entrada_A & Entrada_B;  // AND_Gate _010, 3 bits wide
  assign _011_out = ~(Entrada_A & Entrada_B);  // NAND_Gate _011, 3 bits wide
  assign _100_out = Entrada_B ^ Entrada_A;  // XOR_Gate _100, 3 bits wide
  assign _101_out = ~(Entrada_B ^ Entrada_A);  // XNOR_Gate _101, 3 bits wide
  assign and_1_out = {3{not_10_out[2]}} & {3{not_2_out[2]}} & {3{not_11_out[2]}} & _000_out;  // AND_Gate and_1, 3 bits wide
  assign and_2_out = {3{Chave[0]}} & {3{not_3_out[2]}} & {3{not_4_out[2]}} & _001_out;  // AND_Gate and_2, 3 bits wide
  assign and_3_out = {3{not_5_out[2]}} & {3{Chave[1]}} & {3{not_6_out[2]}} & _010_out;  // AND_Gate and_3, 3 bits wide
  assign and_4_out = {3{Chave[1]}} & {3{Chave[0]}} & {3{not_7_out[2]}} & _011_out;  // AND_Gate and_4, 3 bits wide
  assign and_5_out = {3{Chave[2]}} & {3{not_8_out[2]}} & {3{not_9_out[2]}} & _100_out;  // AND_Gate and_5, 3 bits wide
  assign and_6_out = {3{not_1_out[2]}} & {3{Chave[2]}} & {3{Chave[0]}} & _101_out;  // AND_Gate and_6, 3 bits wide
  assign Saida_S = and_1_out | and_2_out | and_3_out | and_4_out | and_5_out | and_6_out;  // OR_Gate or_1, 3 bits wide
endmodule
