// Logisim project 0302.circ as structural Verilog: 1 circuit, main circuit main
module main (
  input  chave,
  input  a,
  input  b,
  input  c,
  input  d,
  output out_6
);

  wire and_1_out, and_2_out, and_3_out, not_1_out, or_1_out;

  and and_1 (and_1_out, a, c, d);
  or or_1 (or_1_out, a, b, c, d);
  and and_2 (and_2_out, and_1_out, chave);
  and and_3 (and_3_out, or_1_out, not_1_out);
  not not_1 (not_1_out, chave);
  or or_2 (out_6, and_2_out, and_3_out);

  // Notes on the sheet:
  //   Chave
  //   0 = OR
  //   1 = AND
endmodule
