// Logisim project 0303.circ as structural Verilog: 1 circuit, main circuit main
module main (
  input  chave,
  input  grupo,
  input  a,
  input  b,
  input  c,
  input  d,
  output out_7
);

  wire and_1_out, and_2_out, and_3_out, and_4_out, and_5_out, and_6_out, and_7_out, nand_1_out, nor_1_out,
       not_1_out, not_2_out, not_3_out, or_1_out, or_2_out, or_3_out;

  and and_1 (and_1_out, a, c, d);
  or or_1 (or_1_out, a, b, c, d);
  nand nand_1 (nand_1_out, a, b, c, d);
  nor nor_1 (nor_1_out, a, b, c, d);
  and and_2 (and_2_out, and_1_out, chave);
  and and_3 (and_3_out, or_1_out, not_1_out);
  not not_1 (not_1_out, chave);
  and and_4 (and_4_out, nand_1_out, not_2_out);
  not not_2 (not_2_out, chave);
  and and_5 (and_5_out, nor_1_out, chave);
  or or_2 (or_2_out, and_2_out, and_3_out);
  or or_3 (or_3_out, and_4_out, and_5_out);
  not not_3 (not_3_out, grupo);
  and and_6 (and_6_out, or_2_out, not_3_out);
  and and_7 (and_7_out, grupo, or_3_out);
  or or_4 (out_7, and_6_out, and_7_out);

  // Notes on the sheet:
  //   Chave
  //   0 = OR
  //   1 = AND
  //   Grupo
  //   0 = AND/OR
  //   1 = NAND/NOR
endmodule
