// Logisim project 0305.circ as structural Verilog: 1 circuit, main circuit main
module main (
  input  a,
  input  b,
  input  in_3,
  input  in_4,
  input  in_5,
  output out_6
);

  wire and_1_out, and_2_out, and_3_out, and_4_out, and_5_out, and_6_out, and_7_out, and_8_out, and_9_out,
       nand_1_out, nor_1_out, not_1_out, not_2_out, not_3_out, not_4_out, not_5_out, not_6_out, not_7_out,
       not_8_out, not_9_out, not_10_out, not_11_out, not_12_out, not_13_out, not_14_out, or_1_out,
       xnor_1_out, xor_1_out;

  and and_1 (and_1_out, a, b);
  or or_1 (or_1_out, a, b);
  nand nand_1 (nand_1_out, a, b);
  nor nor_1 (nor_1_out, a, b);
  xor xor_1 (xor_1_out, a, b);
  xnor xnor_1 (xnor_1_out, a, b);
  not not_1 (not_1_out, a);
  not not_2 (not_2_out, b);
  not not_3 (not_3_out, in_3);
  not not_4 (not_4_out, in_4);
  not not_5 (not_5_out, in_3);
  not not_6 (not_6_out, in_5);
  not not_7 (not_7_out, in_3);
  not not_8 (not_8_out, in_4);
  not not_9 (not_9_out, in_5);
  not not_10 (not_10_out, in_4);
  not not_11 (not_11_out, in_5);
  not not_12 (not_12_out, in_4);
  not not_13 (not_13_out, in_5);
  and and_2 (and_2_out, not_12_out, not_13_out, and_1_out, not_14_out);
  not not_14 (not_14_out, in_3);
  and and_3 (and_3_out, or_1_out, not_3_out, not_4_out, in_5);
  and and_4 (and_4_out, not_5_out, in_4, nand_1_out, not_6_out);
  and and_5 (and_5_out, not_7_out, nor_1_out, in_4, in_5);
  and and_6 (and_6_out, in_3, xor_1_out, not_8_out, not_9_out);
  and and_7 (and_7_out, in_3, not_10_out, xnor_1_out, in_5);
  and and_8 (and_8_out, in_3, in_4, not_1_out, not_11_out);
  and and_9 (and_9_out, in_3, not_2_out, in_4, in_5);
  or or_2 (out_6, and_3_out, and_4_out, and_5_out, and_6_out, and_8_out, and_2_out, and_9_out);

  // Notes on the sheet:
  //   OP
endmodule
