// Logisim project exemplo0032.circ as structural Verilog: 1 circuit, main circuit main
module main (
  input  [1:0] in_1,
  input  [1:0] in_2,
  input  [1:0] chave,
  output [1:0] out_4,
  output [1:0] out_5,
  output [1:0] out_6
);

  wire [1:0] and_2_out, and_3_out, not_1_out;

  assign out_4 = in_1 & in_2;  // AND_Gate and_1, 2 bits wide
  assign out_6 = in_1 | in_2;  // OR_Gate or_1, 2 bits wide
  assign not_1_out = ~chave;  // NOT_Gate not_1, 2 bits wide
  assign and_2_out = out_4 & chave;  // AND_Gate and_2, 2 bits wide
  assign and_3_out = out_6 & not_1_out;  // AND_Gate and_3, 2 bits wide
  assign out_5 = and_2_out | and_3_out;  // OR_Gate or_2, 2 bits wide

  // Notes on the sheet:
  //   0 = OR
  //   1 = AND
  //   Lucas Siqueira Chagas - 380783
  //   exercicio 02
  //   a partir daqui desse exercicio, fiquei em duvida se era para fazer a comparaçao entre dois bits ou se era para comparar duas entradas de dois bits
  //   mas a unica diferença sera mudar a opçao "entrada de bits" nas entradas, saidas e portas
endmodule
