// Logisim project exemplo0034.circ as structural Verilog: 1 circuit, main circuit main
module main (
  input  in_1,
  input  in_2,
  input  chave,
  output out_4,
  output OR___XOR,
  output out_6,
  output out_7,
  output NOR___XNOR,
  output out_9
);

  wire and_1_out, and_2_out, and_3_out, and_4_out, not_1_out, not_2_out;

  or or_1 (out_4, in_1, in_2);
  xor xor_1 (out_6, in_1, in_2);
  nor nor_1 (out_7, in_1, in_2);
  xnor xnor_1 (out_9, in_1, in_2);
  and and_1 (and_1_out, out_4, not_1_out);
  not not_1 (not_1_out, chave);
  and and_2 (and_2_out, out_6, chave);
  and and_3 (and_3_out, out_7, not_2_out);
  not not_2 (not_2_out, chave);
  and and_4 (and_4_out, out_9, chave);
  or or_2 (OR___XOR, and_1_out, and_2_out);
  or or_3 (NOR___XNOR, and_3_out, and_4_out);

  // Notes on the sheet:
  //   Lucas Siqueira Chagas - 380783
  //   exercicio 04
  //   NO ENUNCIADO, MANDA FAZER SAIDAS SIMULTANEAS, MAS NA SUGESTÃO MANDA FAZER CHAVE INDIVIDUAL
  //   FIZ DE ACORDO COM O ENUNCIADO
  //   0 = OR / NOR
  //   1 = NOR/XNOR
endmodule
