// Logisim project exemplo0037.circ as structural Verilog: 1 circuit, main circuit main
module main (
  input  in_1,
  input  in_2,
  input  in_3,
  input  in_4,
  input  in_5,
  input  in_6,
  input  in_7,
  input  in_8,
  input  _1_para_maior,
  output out_10,
  output se_maior_ascende,
  output saida_final,
  output out_13,
  output out_14,
  output out_15,
  output out_16,
  output out_17,
  output out_18,
  output out_19,
  output out_20
);

  wire and_5_out, and_6_out, and_7_out, not_1_out, not_2_out, not_3_out, xnor_1_out;

  xor xor_1 (out_14, in_1, in_5);
  xor xor_2 (out_16, in_2, in_6);
  xor xor_3 (out_18, in_3, in_7);
  xor xor_4 (out_20, in_4, in_8);
  or or_1 (out_10, out_20, out_18, out_16, out_14);
  and and_1 (out_13, in_1, out_14);
  not not_1 (not_1_out, out_14);
  and and_2 (out_15, in_2, out_16);
  not not_2 (not_2_out, out_16);
  and and_3 (out_17, in_3, out_18);
  not not_3 (not_3_out, out_18);
  and and_4 (out_19, in_4, out_20);
  and and_5 (and_5_out, not_1_out, not_2_out, out_17);
  or or_2 (se_maior_ascende, out_13, and_6_out, and_5_out, and_7_out);
  and and_6 (and_6_out, not_1_out, out_15);
  and and_7 (and_7_out, not_1_out, not_3_out, out_19, not_2_out);
  xnor xnor_1 (xnor_1_out, se_maior_ascende, _1_para_maior);
  and and_8 (saida_final, out_10, xnor_1_out);

  // Notes on the sheet:
  //   exercicio 07
  //   Lucas Siqueira Chagas - 380783
  //   0 para menor
  //   se diferente ascende
endmodule
