// Logisim project exemplo00372.circ as structural Verilog: 1 circuit, main circuit main
module main (
  input  in_1,
  input  in_2,
  input  in_3,
  input  in_4,
  input  in_5,
  input  in_6,
  input  in_7,
  input  in_8,
  output out_9,
  output out_10,
  output out_11,
  output out_12,
  output out_13,
  output out_14,
  output out_15,
  output out_16,
  output out_17
);

  wire and_5_out, and_6_out, and_7_out, not_1_out, not_2_out, not_3_out;

  xor xor_1 (out_10, in_1, in_5);
  xor xor_2 (out_13, in_2, in_6);
  xor xor_3 (out_15, in_3, in_7);
  xor xor_4 (out_17, in_4, in_8);
  and and_1 (out_9, in_1, out_10);
  and and_2 (out_12, in_2, out_13);
  and and_3 (out_14, in_3, out_15);
  and and_4 (out_16, in_4, out_17);
  not not_1 (not_1_out, out_10);
  and and_5 (and_5_out, not_1_out, out_12);
  not not_2 (not_2_out, out_13);
  and and_6 (and_6_out, not_2_out, out_14);
  not not_3 (not_3_out, out_15);
  and and_7 (and_7_out, not_3_out, out_16);
  or or_1 (out_11, out_9, and_5_out, and_6_out, and_7_out);

  // Notes on the sheet:
  //   Lucas Siqueira Chagas - 380783
  //   exercicio 07
endmodule
