// Logisim project Exemplo0031.circ as structural Verilog: 1 circuit, main circuit Exemplo0031
module Exemplo0031 (
  input  [3:0] a,
  input  [3:0] b,
  output [3:0] s,
  output [3:0] s1
);

  assign s = b & a;  // AND_Gate AND, 4 bits wide
  assign s1 = b | a;  // OR_Gate OR, 4 bits wide

  // Notes on the sheet:
  //   Exemplo0031
endmodule
