// Logisim project Exemplo0034.circ as structural Verilog: 2 circuits, main circuit main
module main (
  input  [1:0] a,
  input  [1:0] b,
  input  Flag1,
  input  Flag2,
  output [1:0] Saida
);

  wire [1:0] multiplexador_1_s, multiplexador_2_s, nor_1_out, or_1_out, xnor_1_out, xor_1_out;

  assign or_1_out = b | a;  // OR_Gate or_1, 2 bits wide
  assign xor_1_out = b ^ a;  // XOR_Gate xor_1, 2 bits wide
  assign nor_1_out = ~(b | a);  // NOR_Gate nor_1, 2 bits wide
  // Probe on or_1_out
  // Probe on xor_1_out
  // Probe on nor_1_out
  // Probe on xnor_1_out
  assign xnor_1_out = ~(b ^ a);  // XNOR_Gate xnor_1, 2 bits wide
  Multiplexador multiplexador_1 (.a(xor_1_out), .b(or_1_out), .chave(Flag1), .S(multiplexador_1_s));
  Multiplexador multiplexador_2 (.a(xnor_1_out), .b(nor_1_out), .chave(Flag1), .S(multiplexador_2_s));
  Multiplexador multiplexador_3 (.a(multiplexador_2_s), .b(multiplexador_1_s), .chave(Flag2), .S(Saida));

  // Notes on the sheet:
  //               01 - Nor
  //               10 - Xor
  //                  11 - Xnor
  //   00 - Or
endmodule

module Multiplexador (
  input  [1:0] a,
  input  [1:0] b,
  input  chave,
  output [1:0] S
);

  wire [1:0] and_1_out, and_2_out, not_1_out;

  assign not_1_out = ~{2{chave}};  // NOT_Gate not_1, 2 bits wide
  assign and_1_out = a & {2{chave}};  // AND_Gate and_1, 2 bits wide
  assign and_2_out = b & not_1_out;  // AND_Gate and_2, 2 bits wide
  assign S = and_1_out | and_2_out;  // OR_Gate or_1, 2 bits wide
endmodule
