// Logisim project Exemplo0031.circ as structural Verilog: 1 circuit, main circuit main
module main (
  input  [3:0] a,
  input  [3:0] b,
  output [3:0] s1,
  output [3:0] s2
);

  assign s1 = a & b;  // AND_Gate and1, 4 bits wide
  assign s2 = a | b;  // OR_Gate or1, 4 bits wide
endmodule
