// Logisim project Exemplo0032.circ as structural Verilog: 2 circuits, main circuit main
// w1
module main (
  input  [1:0] A,
  input  [1:0] B,
  input  [1:0] C,
  output [1:0] S0
);

  wire [1:0] and1_2_out, and1_out, and2_out, and3_out, or1_out;

  assign and1_out = A & B;  // AND_Gate and1, 2 bits wide
  assign or1_out = B | A;  // OR_Gate or1, 2 bits wide
  assign and1_2_out = ~C;  // NOT_Gate and1_2, 2 bits wide
  assign and2_out = and1_out & C;  // AND_Gate and2, 2 bits wide
  assign and3_out = or1_out & and1_2_out;  // AND_Gate and3, 2 bits wide
  assign S0 = and2_out | and3_out;  // OR_Gate or2, 2 bits wide

  // Notes on the sheet:
  //   x
  //   y
  //   w1
  //   w2
endmodule

module and_or (
  input  [1:0] X,
  input  [1:0] Y,
  output [1:0] s1,
  output [1:0] S2
);

  assign s1 = X & Y;  // AND_Gate and1, 2 bits wide
  assign S2 = X | Y;  // OR_Gate or1, 2 bits wide
endmodule
