// Logisim project Exemplo0034.circ as structural Verilog: 3 circuits, main circuit main
module main (
  input  [1:0] A,
  input  [1:0] B,
  input  [1:0] C,
  output S0,
  output S1
);

  wire AND1_out, AND2_out, AND3_out, AND4_out, NOT1_out, NOT2_out, OR_NOR_out_3, OR_NOR_out_4, OR_NOR_out_5,
       OR_NOR_out_6, XOR__XNOR_out_3, XOR__XNOR_out_4, XOR__XNOR_out_5, XOR__XNOR_out_6;

  OR_NOR OR_NOR (.A(A), .B(B), .out_3(OR_NOR_out_3), .out_4(OR_NOR_out_4), .out_5(OR_NOR_out_5), .out_6(OR_NOR_out_6));
  XOR_XNOR XOR__XNOR (
    .A(A), .B(B), .out_3(XOR__XNOR_out_3), .out_4(XOR__XNOR_out_4), .out_5(XOR__XNOR_out_5),
    .out_6(XOR__XNOR_out_6));
  not NOT1 (NOT1_out, C[1]);
  not NOT2 (NOT2_out, C[0]);
  and AND1 (AND1_out, OR_NOR_out_3, OR_NOR_out_4, NOT2_out, NOT1_out);
  and AND2 (AND2_out, OR_NOR_out_5, OR_NOR_out_6, C[0], NOT1_out);
  and AND3 (AND3_out, XOR__XNOR_out_3, XOR__XNOR_out_4, NOT2_out, C[1]);
  and AND4 (AND4_out, XOR__XNOR_out_5, XOR__XNOR_out_6, C[1], C[0]);
  or OR1 (S0, AND1_out, AND3_out);
  or OR2 (S1, AND2_out, AND4_out);

  // Notes on the sheet:
  //   00-OR
  //   01-NOR
  //   10-XOR
  //   11-XNOR
  //   w2
  //   w3
  //   w4
  //   w1
endmodule

module XOR_XNOR (
  input  [1:0] A,
  input  [1:0] B,
  output out_3,
  output out_4,
  output out_5,
  output out_6
);

  assign {out_4, out_3} = A ^ B;  // XOR_Gate XOR0, 2 bits wide
  assign {out_6, out_5} = ~(A ^ B);  // XNOR_Gate XNOR0, 2 bits wide
endmodule

module OR_NOR (
  input  [1:0] A,
  input  [1:0] B,
  output out_3,
  output out_4,
  output out_5,
  output out_6
);

  assign {out_4, out_3} = A | B;  // OR_Gate OR0, 2 bits wide
  assign {out_6, out_5} = ~(A | B);  // NOR_Gate NOR0, 2 bits wide
endmodule
