// Logisim project Exemplo0035.circ as structural Verilog: 3 circuits, main circuit main
module main (
  input  [1:0] A,
  input  [1:0] B,
  input  [2:0] C,
  output out_4
);

  wire NAND1_out, NAND2_out, NAND3_out, NAND4_out, NAND5_out, NAND6_out, NAND7_out, NAND8_out, not_1_out,
       not_2_out, not_3_out, notx_noty_and_or_1_out_3, notx_noty_and_or_1_out_4, notx_noty_and_or_1_out_5,
       notx_noty_and_or_1_out_6, notx_noty_and_or_1_out_7, notx_noty_and_or_1_out_8,
       notx_noty_and_or_1_out_9, notx_noty_and_or_1_out_10, OR1_out, OR2_out, xor_xnor_nand_nor_1_out_3,
       xor_xnor_nand_nor_1_out_4, xor_xnor_nand_nor_1_out_5, xor_xnor_nand_nor_1_out_6,
       xor_xnor_nand_nor_1_out_7, xor_xnor_nand_nor_1_out_8, xor_xnor_nand_nor_1_out_9,
       xor_xnor_nand_nor_1_out_10;

  NOTX_NOTY_AND_OR notx_noty_and_or_1 (
    .A(A), .B(B), .out_3(notx_noty_and_or_1_out_3), .out_4(notx_noty_and_or_1_out_4),
    .out_5(notx_noty_and_or_1_out_5), .out_6(notx_noty_and_or_1_out_6), .out_7(notx_noty_and_or_1_out_7),
    .out_8(notx_noty_and_or_1_out_8), .out_9(notx_noty_and_or_1_out_9), .out_10(notx_noty_and_or_1_out_10));
  XOR_XNOR_NAND_NOR xor_xnor_nand_nor_1 (
    .A(A), .B(B), .out_3(xor_xnor_nand_nor_1_out_3), .out_4(xor_xnor_nand_nor_1_out_4),
    .out_5(xor_xnor_nand_nor_1_out_5), .out_6(xor_xnor_nand_nor_1_out_6), .out_7(xor_xnor_nand_nor_1_out_7),
    .out_8(xor_xnor_nand_nor_1_out_8), .out_9(xor_xnor_nand_nor_1_out_9), .out_10(xor_xnor_nand_nor_1_out_10));
  not not_1 (not_1_out, C[2]);
  not not_2 (not_2_out, C[1]);
  not not_3 (not_3_out, C[0]);
  and NAND1 (NAND1_out, notx_noty_and_or_1_out_3, notx_noty_and_or_1_out_4, not_3_out, not_2_out, not_1_out);
  and NAND2 (NAND2_out, notx_noty_and_or_1_out_5, notx_noty_and_or_1_out_6, C[0], not_2_out, not_1_out);
  and NAND3 (NAND3_out, notx_noty_and_or_1_out_7, notx_noty_and_or_1_out_8, not_3_out, C[1], not_1_out);
  and NAND4 (NAND4_out, notx_noty_and_or_1_out_9, notx_noty_and_or_1_out_10, not_3_out, not_2_out, C[2]);
  and NAND5 (NAND5_out, xor_xnor_nand_nor_1_out_3, xor_xnor_nand_nor_1_out_4, C[0], C[1], not_1_out);
  and NAND6 (NAND6_out, xor_xnor_nand_nor_1_out_5, xor_xnor_nand_nor_1_out_6, C[0], not_2_out, C[2]);
  and NAND7 (NAND7_out, xor_xnor_nand_nor_1_out_7, xor_xnor_nand_nor_1_out_8, not_3_out, C[1], C[2]);
  and NAND8 (NAND8_out, xor_xnor_nand_nor_1_out_9, xor_xnor_nand_nor_1_out_10, C[0], C[1], C[2]);
  or OR1 (OR1_out, NAND1_out, NAND2_out, NAND3_out, NAND4_out);
  or OR2 (OR2_out, NAND5_out, NAND6_out, NAND7_out, NAND8_out);
  or OR3 (out_4, OR1_out, OR2_out);

  // Notes on the sheet:
  //   NOTX/NOTY
  //   AND/OR
  //   XOR/NOR
  //   NAND/NOR
  //   not2
  //   not1
  //   000-NOTX
  //   001-NOTY
  //   010-AND
  //   100-OR
  //   011-XOR
  //   101-XNOR
  //   110-NAND
  //   111-NOR
  //   not3
endmodule

module NOTX_NOTY_AND_OR (
  input  [1:0] A,
  input  [1:0] B,
  output out_3,
  output out_4,
  output out_5,
  output out_6,
  output out_7,
  output out_8,
  output out_9,
  output out_10
);

  assign {out_4, out_3} = ~A;  // NOT_Gate NOTX, 2 bits wide
  assign {out_6, out_5} = ~B;  // NOT_Gate NOTY, 2 bits wide
  assign {out_8, out_7} = A & B;  // AND_Gate and0, 2 bits wide
  assign {out_10, out_9} = A | B;  // OR_Gate or0, 2 bits wide
endmodule

module XOR_XNOR_NAND_NOR (
  input  [1:0] A,
  input  [1:0] B,
  output out_3,
  output out_4,
  output out_5,
  output out_6,
  output out_7,
  output out_8,
  output out_9,
  output out_10
);

  assign {out_4, out_3} = A ^ B;  // XOR_Gate xor1, 2 bits wide
  assign {out_6, out_5} = ~(A ^ B);  // XNOR_Gate xnor, 2 bits wide
  assign {out_8, out_7} = ~(A & B);  // NAND_Gate nand1, 2 bits wide
  assign {out_10, out_9} = ~(A | B);  // NOR_Gate nor1, 2 bits wide
endmodule
