// Logisim project sim02.circ as structural Verilog: 1 circuit, main circuit main
module main (
  input  in_1,
  input  a0,
  input  a1,
  input  b0,
  input  b1,
  output out_6,
  output out_7
);

  wire and_1_out, and_2_out, and_3_out, and_4_out, and_5_out, and_6_out, not_1_out, not_2_out, or_1_out,
       or_2_out;

  or or_1 (or_1_out, b0, a0);
  and and_1 (and_1_out, b0, a0);
  or or_2 (or_2_out, b1, a1);
  and and_2 (and_2_out, b1, a1);
  not not_1 (not_1_out, in_1);
  and and_3 (and_3_out, not_1_out, or_1_out);
  and and_4 (and_4_out, in_1, and_1_out);
  not not_2 (not_2_out, in_1);
  and and_5 (and_5_out, not_2_out, or_2_out);
  and and_6 (and_6_out, in_1, and_2_out);
  or or_3 (out_6, and_3_out, and_4_out);
  or or_4 (out_7, and_5_out, and_6_out);
endmodule
