// Logisim project sim04.circ as structural Verilog: 1 circuit, main circuit main
module main (
  input  in_1,
  input  in_2,
  input  a0,
  input  a1,
  input  b0,
  input  b1,
  output out_7,
  output out_8
);

  wire _0r1_out, and3_out, and4_out, and5_out, and6_out, not_1_out, not_2_out, or2_out, xor_1_out, xor_2_out,
       xor_3_out, xor_4_out, xor_5_out, xor_6_out;

  or _0r1 (_0r1_out, b0, a0);
  xor xor_1 (xor_1_out, b0, a0);
  or or2 (or2_out, b1, a1);
  xor xor_2 (xor_2_out, b1, a1);
  xor xor_3 (xor_3_out, in_2, _0r1_out);
  xor xor_4 (xor_4_out, in_2, xor_1_out);
  xor xor_5 (xor_5_out, in_2, or2_out);
  xor xor_6 (xor_6_out, in_2, xor_2_out);
  not not_1 (not_1_out, in_1);
  and and3 (and3_out, not_1_out, xor_3_out);
  and and4 (and4_out, in_1, xor_4_out);
  not not_2 (not_2_out, in_1);
  and and5 (and5_out, not_2_out, xor_5_out);
  and and6 (and6_out, in_1, xor_6_out);
  or or_1 (out_7, and3_out, and4_out);
  or or_2 (out_8, and5_out, and6_out);
endmodule
