// Logisim project sim06.circ as structural Verilog: 1 circuit, main circuit main
module main (
  input  in_1,
  input  in_2,
  input  in_3,
  input  in_4,
  input  in_5,
  output out_6
);

  wire and_1_out, and_2_out, and_3_out;

  and and_1 (and_1_out, in_2, in_3);
  and and_2 (and_2_out, in_4, in_5);
  and and_3 (and_3_out, and_1_out, and_2_out);
  xor xor_1 (out_6, in_1, and_3_out);
endmodule
