// Logisim project Guia04.circ as structural Verilog: 7 circuits, main circuit Full Adder
module Full_Adder (
  input  a,
  input  b,
  input  c,
  output carry_out,
  output s0
);

  wire and_1_out, and_2_out, xor_2_out;

  and and_1 (and_1_out, c, xor_2_out);
  or or_1 (carry_out, and_2_out, and_1_out);
  and and_2 (and_2_out, a, b);
  xor xor_1 (s0, c, xor_2_out);
  xor xor_2 (xor_2_out, a, b);
endmodule

module Full_Adder_4_Bit (
  input  ca,
  input  cb,
  input  a2,
  input  b2,
  input  a1,
  input  b1,
  input  a0,
  input  b0,
  output cout,
  output s2,
  output s1,
  output s0
);

  wire full_adder_2_carry_out, full_adder_3_carry_out, or_1_out;

  or or_1 (or_1_out, ca, cb);
  Full_Adder full_adder_1 (.c(full_adder_2_carry_out), .a(a2), .b(b2), .carry_out(cout), .s0(s2));
  Full_Adder full_adder_2 (.c(full_adder_3_carry_out), .a(a1), .b(b1), .carry_out(full_adder_2_carry_out), .s0(s1));
  Full_Adder full_adder_3 (.c(or_1_out), .a(a0), .b(b0), .carry_out(full_adder_3_carry_out), .s0(s0));
endmodule

module Full_Subtractor (
  input  a0,
  input  b0,
  input  cin,
  output out_4,
  output s
);

  wire and_1_out, and_2_out, and_3_out, not_1_out, xor_1_out;

  or or_1 (out_4, and_1_out, and_2_out, and_3_out);
  and and_1 (and_1_out, not_1_out, cin);
  and and_2 (and_2_out, not_1_out, b0);
  and and_3 (and_3_out, b0, cin);
  not not_1 (not_1_out, a0);
  xor xor_1 (xor_1_out, a0, b0);
  xor xor_2 (s, xor_1_out, cin);
endmodule

module Full_Subtractor_4_Bit (
  input  ca,
  input  cb,
  input  a2,
  input  b2,
  input  a1,
  input  b1,
  input  a0,
  input  b0,
  output s3,
  output s2,
  output s1,
  output s0
);

  wire full_subtractor_2_out_4, full_subtractor_3_out_4, or_1_out;

  or or_1 (or_1_out, ca, cb);
  Full_Subtractor full_subtractor_1 (.out_4(s3), .a0(a2), .b0(b2), .s(s2), .cin(full_subtractor_3_out_4));
  Full_Subtractor full_subtractor_2 (.out_4(full_subtractor_2_out_4), .a0(a0), .b0(b0), .s(s0), .cin(or_1_out));
  Full_Subtractor full_subtractor_3 (
    .out_4(full_subtractor_3_out_4), .a0(a1), .b0(b1), .s(s1), .cin(full_subtractor_2_out_4));
endmodule

module Equals_4_Bit (
  input  a,
  input  a_2,
  input  a_3,
  input  a_4,
  input  b,
  input  b_2,
  input  b_3,
  input  b_4,
  output out_9
);

  wire xnor_1_out, xnor_2_out, xnor_3_out, xnor_4_out;

  xnor xnor_1 (xnor_1_out, a, b);
  xnor xnor_2 (xnor_2_out, a_2, b_2);
  xnor xnor_3 (xnor_3_out, a_3, b_3);
  xnor xnor_4 (xnor_4_out, b_4, a_4);
  and and_1 (out_9, xnor_1_out, xnor_2_out, xnor_3_out, xnor_4_out);
endmodule

module Different_4_Bit (
  input  a,
  input  a_2,
  input  a_3,
  input  a_4,
  input  b,
  input  b_2,
  input  b_3,
  input  b_4,
  output out_9
);

  wire xor_1_out, xor_2_out, xor_3_out, xor_4_out;

  xor xor_1 (xor_1_out, a, b);
  xor xor_2 (xor_2_out, a_2, b_2);
  xor xor_3 (xor_3_out, a_3, b_3);
  xor xor_4 (xor_4_out, a_4, b_4);
  or or_1 (out_9, xor_1_out, xor_2_out, xor_3_out, xor_4_out);
endmodule

module Complement_4_Bit (
  input  a3,
  input  a2,
  input  a1,
  input  a0,
  output carry_out,
  output s3,
  output s2,
  output s1,
  output s0
);

  wire full_adder_2_carry_out, full_adder_3_carry_out, full_adder_4_carry_out, not_1_out, not_2_out,
       not_3_out, not_4_out;

  not not_1 (not_1_out, a3);
  not not_2 (not_2_out, a1);
  not not_3 (not_3_out, a2);
  not not_4 (not_4_out, a0);
  Full_Adder full_adder_1 (.c(full_adder_2_carry_out), .a(not_1_out), .b(1'b0), .carry_out(carry_out), .s0(s3));
  Full_Adder full_adder_2 (
    .c(full_adder_3_carry_out), .a(not_3_out), .b(1'b0), .carry_out(full_adder_2_carry_out), .s0(s2));
  Full_Adder full_adder_3 (
    .c(full_adder_4_carry_out), .a(not_2_out), .b(1'b0), .carry_out(full_adder_3_carry_out), .s0(s1));
  Full_Adder full_adder_4 (.c(1'b0), .a(not_4_out), .b(1'b1), .carry_out(full_adder_4_carry_out), .s0(s0));
endmodule
