// Logisim project Exemplo0042.circ as structural Verilog: 3 circuits, main circuit main
// H.A.
module HalfAdder (
  input  a,
  input  b,
  output s1,
  output s0
);

  and and_1 (s1, a, b);
  xor xor_1 (s0, a, b);
endmodule

// F.A.
module FullAdder (
  input  a,
  input  b,
  input  carry_In,
  output carry_Out,
  output s
);

  wire halfadder_1_s0, halfadder_1_s1, halfadder_2_s1;

  or or_1 (carry_Out, halfadder_1_s1, halfadder_2_s1);
  HalfAdder halfadder_1 (.a(a), .b(b), .s1(halfadder_1_s1), .s0(halfadder_1_s0));
  HalfAdder halfadder_2 (.a(halfadder_1_s0), .b(carry_In), .s1(halfadder_2_s1), .s0(s));
endmodule

module main (
  input  [2:0] a,
  input  [2:0] b,
  input  carry_In,
  output [3:0] s
);

  wire fulladder_1_carry_out, fulladder_2_carry_out, fulladder_3_carry_out, xor_2_out, xor_3_out, xor_4_out;

  // Probe on a
  xor xor_1 (s[3], carry_In, fulladder_1_carry_out);
  // Probe on b
  xor xor_2 (xor_2_out, b[2], carry_In);
  FullAdder fulladder_1 (
    .carry_Out(fulladder_1_carry_out), .a(a[2]), .b(xor_2_out), .s(s[2]), .carry_In(fulladder_2_carry_out));
  // Probe on s
  xor xor_3 (xor_3_out, b[0], carry_In);
  xor xor_4 (xor_4_out, b[1], carry_In);
  FullAdder fulladder_2 (
    .carry_Out(fulladder_2_carry_out), .a(a[1]), .b(xor_4_out), .s(s[1]), .carry_In(fulladder_3_carry_out));
  FullAdder fulladder_3 (.carry_Out(fulladder_3_carry_out), .a(a[0]), .b(xor_3_out), .s(s[0]), .carry_In(carry_In));
  // Probe on s
endmodule
