// Logisim project Exemplo0044.circ as structural Verilog: 1 circuit, main circuit main
module main (
  input  [3:0] a,
  input  [3:0] b,
  output out_3
);

  wire [3:0] xnor_1_out;

  assign xnor_1_out = ~(a ^ b);  // XNOR_Gate xnor_1, 4 bits wide
  nand nand_1 (out_3, xnor_1_out[3], xnor_1_out[2], xnor_1_out[1], xnor_1_out[0]);
endmodule
