// Logisim project Exemplo0045.circ as structural Verilog: 4 circuits, main circuit main
module main (
  input  [3:0] a,
  output overFlow,
  output [3:0] complemento
);

  // Probe on a
  _2complement u_2complement_1 (.OverFlow(overFlow), .in_1(a), .s(complemento));
  // Probe on complemento
endmodule

// H.A
module halfAdder (
  input  a,
  input  b,
  output s1,
  output s0
);

  and and_1 (s1, a, b);
  xor xor_1 (s0, a, b);
endmodule

// F.A
module fullAdder (
  input  a,
  input  b,
  input  carryIn,
  output carryOut,
  output s
);

  wire halfadder_1_s0, halfadder_1_s1, halfadder_2_s1;

  or or_1 (carryOut, halfadder_1_s1, halfadder_2_s1);
  halfAdder halfadder_1 (.a(a), .b(b), .s1(halfadder_1_s1), .s0(halfadder_1_s0));
  halfAdder halfadder_2 (.a(halfadder_1_s0), .b(carryIn), .s1(halfadder_2_s1), .s0(s));
endmodule

// c2
module _2complement (
  input  [3:0] in_1,
  output OverFlow,
  output [3:0] s
);

  wire fulladder_2_carryout, fulladder_3_carryout, fulladder_4_carryout;
  wire [3:0] not_1_out;

  fullAdder fulladder_1 (.carryOut(OverFlow), .a(not_1_out[3]), .b(1'b0), .s(s[3]), .carryIn(fulladder_2_carryout));
  fullAdder fulladder_2 (
    .carryOut(fulladder_2_carryout), .a(not_1_out[2]), .b(1'b0), .s(s[2]), .carryIn(fulladder_3_carryout));
  assign not_1_out = ~in_1;  // NOT_Gate not_1, 4 bits wide
  fullAdder fulladder_3 (
    .carryOut(fulladder_3_carryout), .a(not_1_out[1]), .b(1'b0), .s(s[1]), .carryIn(fulladder_4_carryout));
  fullAdder fulladder_4 (.carryOut(fulladder_4_carryout), .a(not_1_out[0]), .b(1'b0), .s(s[0]), .carryIn(1'b1));
endmodule
