// Logisim project Exemplo0046.circ as structural Verilog: 3 circuits, main circuit main
module main (
  input  [2:0] a,
  input  [2:0] b,
  input  carry_In,
  output [3:0] s
);

  wire fulladder_1_carryout, fulladder_2_carryout, fulladder_3_carryout, xor_2_out, xor_3_out, xor_4_out;

  // Probe on a
  xor xor_1 (s[3], carry_In, fulladder_1_carryout);
  xor xor_2 (xor_2_out, b[2], carry_In);
  fullAdder fulladder_1 (
    .carryOut(fulladder_1_carryout), .a(a[2]), .b(xor_2_out), .s(s[2]), .carryIn(fulladder_3_carryout));
  // Probe on s
  // Probe on b
  xor xor_3 (xor_3_out, b[0], carry_In);
  xor xor_4 (xor_4_out, b[1], carry_In);
  fullAdder fulladder_2 (.carryOut(fulladder_2_carryout), .a(a[0]), .b(xor_3_out), .s(s[0]), .carryIn(carry_In));
  fullAdder fulladder_3 (
    .carryOut(fulladder_3_carryout), .a(a[1]), .b(xor_4_out), .s(s[1]), .carryIn(fulladder_2_carryout));
endmodule

// H.A
module halfAdder (
  input  a,
  input  b,
  output s1,
  output s0
);

  and and_1 (s1, a, b);
  xor xor_1 (s0, a, b);
endmodule

// F.A.
module fullAdder (
  input  a,
  input  b,
  input  carryIn,
  output carryOut,
  output s
);

  wire halfadder_1_s0, halfadder_1_s1, halfadder_2_s1;

  or or_1 (carryOut, halfadder_1_s1, halfadder_2_s1);
  halfAdder halfadder_1 (.a(a), .b(b), .s1(halfadder_1_s1), .s0(halfadder_1_s0));
  halfAdder halfadder_2 (.a(halfadder_1_s0), .b(carryIn), .s1(halfadder_2_s1), .s0(s));
endmodule
