// Logisim project Exemplo0047.circ as structural Verilog: 1 circuit, main circuit main
module main (
  input  [3:0] in_1,
  input  [3:0] in_2,
  input  chave,
  output out_4
);

  wire and_1_out, and_2_out, and_3_out, not_1_out, not_2_out;
  wire [3:0] xnor_1_out;

  assign xnor_1_out = ~(in_1 ^ in_2);  // XNOR_Gate xnor_1, 4 bits wide
  and and_1 (and_1_out, xnor_1_out[3], xnor_1_out[2], xnor_1_out[1], xnor_1_out[0]);
  not not_1 (not_1_out, and_1_out);
  not not_2 (not_2_out, chave);
  and and_2 (and_2_out, chave, not_1_out);
  or or_1 (out_4, and_2_out, and_3_out);
  and and_3 (and_3_out, and_1_out, not_2_out);
endmodule
