// Logisim project Exemplo0038.circ as structural Verilog: 3 circuits, main circuit main
module main (
  input  a1,
  input  a2,
  input  a3,
  input  a4,
  input  b1,
  input  b2,
  input  b3,
  input  b4,
  output s3,
  output s2,
  output s1,
  output s0,
  output Carry_out
);

  wire full_adder_2_vai_1, full_adder_3_vai_1, meia_soma_1_s1;

  Full_Adder full_adder_1 (.a(a4), .b(b4), .vem_1(full_adder_2_vai_1), .soma(s3), .vai_1(Carry_out));
  Full_Adder full_adder_2 (.a(a3), .b(b3), .vem_1(full_adder_3_vai_1), .soma(s2), .vai_1(full_adder_2_vai_1));
  Full_Adder full_adder_3 (.a(a2), .b(b2), .vem_1(meia_soma_1_s1), .soma(s1), .vai_1(full_adder_3_vai_1));
  meia_soma meia_soma_1 (.A(a1), .B(b1), .s0(s0), .s1(meia_soma_1_s1));
endmodule

// F.A
module Full_Adder (
  input  a,
  input  b,
  input  vem_1,
  output soma,
  output vai_1
);

  wire meia_soma_1_s0, meia_soma_1_s1;

  meia_soma meia_soma_1 (.A(a), .B(b), .s0(meia_soma_1_s0), .s1(meia_soma_1_s1));
  meia_soma meia_soma_2 (.A(meia_soma_1_s0), .B(vem_1), .s0(soma));  // open: s1
  or or_1 (vai_1, meia_soma_1_s0, meia_soma_1_s1);
endmodule

// H.A
module meia_soma (
  input  A,
  input  B,
  output s0,
  output s1
);

  xor xor_1 (s0, A, B);
  and and_1 (s1, A, B);
endmodule
