// Logisim project Exemplo0039.circ as structural Verilog: 3 circuits, main circuit main
module main (
  input  a1,
  input  a2,
  input  a3,
  input  a4,
  input  b1,
  input  b2,
  input  b3,
  input  b4,
  output s3,
  output s2,
  output s1,
  output s0,
  output Carry_out
);

  wire full_subtractor_2_vai_1, full_subtractor_3_vai_1, meia_sub_1_s1;

  Full_Subtractor full_subtractor_1 (.a(a4), .b(b4), .vem_1(full_subtractor_2_vai_1), .soma(s3), .vai_1(Carry_out));
  Full_Subtractor full_subtractor_2 (
    .a(a3), .b(b3), .vem_1(full_subtractor_3_vai_1), .soma(s2), .vai_1(full_subtractor_2_vai_1));
  Full_Subtractor full_subtractor_3 (.a(a2), .b(b2), .vem_1(meia_sub_1_s1), .soma(s1), .vai_1(full_subtractor_3_vai_1));
  meia_sub meia_sub_1 (.A(a1), .B(b1), .s0(s0), .s1(meia_sub_1_s1));
endmodule

// F.S
module Full_Subtractor (
  input  a,
  input  b,
  input  vem_1,
  output soma,
  output vai_1
);

  wire and_1_out, and_2_out, not_1_out, not_2_out, xor_1_out;

  not not_1 (not_1_out, a);
  xor xor_1 (xor_1_out, b, a);
  and and_1 (and_1_out, b, not_1_out);
  not not_2 (not_2_out, xor_1_out);
  xor xor_2 (soma, vem_1, xor_1_out);
  and and_2 (and_2_out, vem_1, not_2_out);
  or or_1 (vai_1, and_2_out, and_1_out);
endmodule

// H.S
module meia_sub (
  input  A,
  input  B,
  output s0,
  output s1
);

  wire not_1_out;

  not not_1 (not_1_out, A);
  xor xor_1 (s0, A, B);
  and and_1 (s1, not_1_out, B);
endmodule
