// Logisim project Exemplo0042.circ as structural Verilog: 5 circuits, main circuit main
module main (
  input  [3:0] A,
  output s1,
  output s2,
  output s3,
  output s4,
  output Carry_out
);

  wire complemento_de_1_1_out_2, complemento_de_1_1_out_3, complemento_de_1_1_out_4, complemento_de_1_1_out_5;

  complemento_de_1 complemento_de_1_1 (
    .in_1(A), .out_2(complemento_de_1_1_out_2), .out_3(complemento_de_1_1_out_3),
    .out_4(complemento_de_1_1_out_4), .out_5(complemento_de_1_1_out_5));
  full_adder_4bits full_adder_4bits_1 (
    .Carry_out(Carry_out), .s3(s4), .s2(s3), .s1(s2), .s0(s1), .a1(complemento_de_1_1_out_2),
    .a2(complemento_de_1_1_out_3), .a3(complemento_de_1_1_out_4), .a4(complemento_de_1_1_out_5), .b1(1'b1),
    .b2(1'b0), .b3(1'b0), .b4(1'b0));
endmodule

// Com1
module complemento_de_1 (
  input  [3:0] in_1,
  output out_2,
  output out_3,
  output out_4,
  output out_5
);

  not not_1 (out_2, in_1[0]);
  not not_2 (out_3, in_1[1]);
  not not_3 (out_4, in_1[2]);
  not not_4 (out_5, in_1[3]);
endmodule

// F.A
module Full_Adder (
  input  a,
  input  b,
  input  vem_1,
  output soma,
  output vai_1
);

  wire and_1_out, and_2_out, xor_1_out;

  xor xor_1 (xor_1_out, b, a);
  and and_1 (and_1_out, b, a);
  xor xor_2 (soma, vem_1, xor_1_out);
  and and_2 (and_2_out, vem_1, xor_1_out);
  or or_1 (vai_1, and_2_out, and_1_out);
endmodule

// F.A 4 btis
module full_adder_4bits (
  input  a1,
  input  a2,
  input  a3,
  input  a4,
  input  b1,
  input  b2,
  input  b3,
  input  b4,
  output s3,
  output s2,
  output s1,
  output s0,
  output Carry_out
);

  wire full_adder_2_vai_1, full_adder_3_vai_1, meia_soma_1_s1;

  Full_Adder full_adder_1 (.a(a4), .b(b4), .vem_1(full_adder_2_vai_1), .soma(s3), .vai_1(Carry_out));
  Full_Adder full_adder_2 (.a(a3), .b(b3), .vem_1(full_adder_3_vai_1), .soma(s2), .vai_1(full_adder_2_vai_1));
  Full_Adder full_adder_3 (.a(a2), .b(b2), .vem_1(meia_soma_1_s1), .soma(s1), .vai_1(full_adder_3_vai_1));
  meia_soma meia_soma_1 (.A(a1), .B(b1), .s0(s0), .s1(meia_soma_1_s1));
endmodule

// H.A
module meia_soma (
  input  A,
  input  B,
  output s0,
  output s1
);

  xor xor_1 (s0, A, B);
  and and_1 (s1, A, B);
endmodule
