// Logisim project Exemplo0021.circ as structural Verilog: 1 circuit, main circuit main
module main (
  input  x,
  input  y,
  input  carryIn,
  input  x_2,
  input  y_2,
  input  carryIn_2,
  input  x_3,
  input  y_3,
  input  carryIn_3,
  input  x_4,
  input  y_4,
  input  carryIn_4,
  output s0,
  output s0_2,
  output carryOut,
  output carryOut_2,
  output s0_3,
  output s0_4,
  output carryOut_3,
  output carryOut_4
);

  wire and_1_out, and_2_out, and_3_out, and_4_out, and_5_out, and_6_out, and_7_out, and_8_out, xor_1_out,
       xor_2_out, xor_5_out, xor_6_out;

  xor xor_1 (xor_1_out, x, y);
  and and_1 (and_1_out, x, y);
  xor xor_2 (xor_2_out, x_3, y_3);
  and and_2 (and_2_out, x_3, y_3);
  xor xor_3 (s0, xor_1_out, carryIn);
  and and_3 (and_3_out, xor_1_out, carryIn);
  xor xor_4 (s0_3, xor_2_out, carryIn_3);
  and and_4 (and_4_out, xor_2_out, carryIn_3);
  or or_1 (carryOut, and_3_out, and_1_out);
  or or_2 (carryOut_3, and_4_out, and_2_out);
  and and_5 (and_5_out, x_2, y_2);
  and and_6 (and_6_out, x_4, y_4);
  xor xor_5 (xor_5_out, x_2, y_2);
  xor xor_6 (xor_6_out, x_4, y_4);
  xor xor_7 (s0_2, xor_5_out, carryIn_2);
  and and_7 (and_7_out, xor_5_out, carryIn_2);
  xor xor_8 (s0_4, xor_6_out, carryIn_4);
  and and_8 (and_8_out, xor_6_out, carryIn_4);
  or or_3 (carryOut_2, and_7_out, and_5_out);
  or or_4 (carryOut_4, and_8_out, and_6_out);
endmodule
