// Logisim project Exemplo0022.circ as structural Verilog: 1 circuit, main circuit main
module main (
  input  x,
  input  y,
  input  z,
  input  x_2,
  input  y_2,
  input  z_2,
  input  x_3,
  input  y_3,
  input  z_3,
  input  x_4,
  input  y_4,
  input  z_4,
  output s0,
  output s0_2,
  output s1,
  output s1_2,
  output s0_3,
  output s0_4,
  output s1_3,
  output s1_4
);

  wire and_1_out, and_2_out, and_3_out, and_4_out, and_5_out, and_6_out, and_7_out, and_8_out, not_1_out,
       not_2_out, not_3_out, not_4_out, not_5_out, not_6_out, not_7_out, not_8_out, or_1_out, or_2_out,
       or_5_out, or_6_out, xor_1_out, xor_2_out, xor_5_out, xor_6_out;

  not not_1 (not_1_out, x);
  not not_2 (not_2_out, x);
  not not_3 (not_3_out, x_3);
  not not_4 (not_4_out, x_3);
  xor xor_1 (xor_1_out, x, y);
  or or_1 (or_1_out, not_1_out, y);
  and and_1 (and_1_out, not_2_out, y);
  xor xor_2 (xor_2_out, x_3, y_3);
  or or_2 (or_2_out, not_3_out, y_3);
  and and_2 (and_2_out, not_4_out, y_3);
  xor xor_3 (s0, xor_1_out, z);
  and and_3 (and_3_out, or_1_out, z);
  xor xor_4 (s0_3, xor_2_out, z_3);
  and and_4 (and_4_out, or_2_out, z_3);
  or or_3 (s1, and_3_out, and_1_out);
  or or_4 (s1_3, and_4_out, and_2_out);
  not not_5 (not_5_out, x_2);
  not not_6 (not_6_out, x_2);
  not not_7 (not_7_out, x_4);
  not not_8 (not_8_out, x_4);
  xor xor_5 (xor_5_out, x_2, y_2);
  or or_5 (or_5_out, not_5_out, y_2);
  and and_5 (and_5_out, not_6_out, y_2);
  xor xor_6 (xor_6_out, x_4, y_4);
  or or_6 (or_6_out, not_7_out, y_4);
  and and_6 (and_6_out, not_8_out, y_4);
  xor xor_7 (s0_2, xor_5_out, z_2);
  and and_7 (and_7_out, or_5_out, z_2);
  xor xor_8 (s0_4, xor_6_out, z_4);
  and and_8 (and_8_out, or_6_out, z_4);
  or or_7 (s1_2, and_7_out, and_5_out);
  or or_8 (s1_4, and_8_out, and_6_out);
endmodule
