// Logisim project Exemplo0027.circ as structural Verilog: 1 circuit, main circuit main
module main (
  input  [5:0] B,
  input  [5:0] A,
  input  OP,
  output S
);

  wire _1_2_out, _1_out, _2_out, _3_out, _4_out, _5_out, _6_out, and1_out, and2_out, not1_out, not2_out;

  xor _1 (_1_out, A[0], B[0]);
  and and1 (and1_out, OP, not1_out);
  xor _2 (_2_out, A[1], B[1]);
  xor _3 (_3_out, A[2], B[2]);
  not not1 (not1_out, _1_2_out);
  xor _4 (_4_out, A[3], B[3]);
  or _1_2 (_1_2_out, _1_out, _2_out, _3_out, _4_out, _5_out, _6_out);
  not not2 (not2_out, OP);
  or _2_2 (S, and1_out, and2_out);
  xor _6 (_6_out, A[5], B[5]);
  xor _5 (_5_out, A[4], B[4]);
  and and2 (and2_out, _1_2_out, not2_out);

  // Notes on the sheet:
  //   Exemplo0027 - João Henrique Mendes de Oliveira - 392734
endmodule
