// Logisim project Exemplo0021.circ as structural Verilog: 2 circuits, main circuit Full Adder
module Full_Adder (
  input  a,
  input  b,
  input  carry_in,
  output s,
  output carry_out
);

  wire and_1_out, and_2_out, xor_1_out;

  and and_1 (and_1_out, a, b);
  xor xor_1 (xor_1_out, b, a);
  and and_2 (and_2_out, xor_1_out, carry_in);
  xor xor_2 (s, carry_in, xor_1_out);
  or or_1 (carry_out, and_2_out, and_1_out);

  // Notes on the sheet:
  //   Alvaro Henrique de Araujo Rungue - 395487
endmodule

module Exemplo0021 (
  input  in_1,
  input  in_2,
  input  in_3,
  input  in_4,
  input  in_5,
  input  in_6,
  input  in_7,
  input  in_8,
  input  in_9,
  output out_10,
  output out_11,
  output out_12,
  output out_13,
  output out_14
);

  wire full_adder_1_carry_out, full_adder_2_carry_out, full_adder_3_carry_out;

  Full_Adder full_adder_1 (.carry_in(in_9), .carry_out(full_adder_1_carry_out), .a(in_1), .b(in_2), .s(out_11));
  Full_Adder full_adder_2 (
    .carry_in(full_adder_1_carry_out), .carry_out(full_adder_2_carry_out), .a(in_3), .b(in_4), .s(out_12));
  Full_Adder full_adder_3 (
    .carry_in(full_adder_2_carry_out), .carry_out(full_adder_3_carry_out), .a(in_5), .b(in_6), .s(out_13));
  Full_Adder full_adder_4 (.carry_in(full_adder_3_carry_out), .carry_out(out_10), .a(in_7), .b(in_8), .s(out_14));

  // Notes on the sheet:
  //   Alvaro Henrique de Araujo Rungue - 395487
endmodule
