// Logisim project Exemplo0022.circ as structural Verilog: 2 circuits, main circuit FullSubtractor
module FullSubtractor (
  input  a,
  input  b,
  input  carry_in,
  output s,
  output carry_out
);

  wire and_1_out, and_2_out, not_1_out, not_2_out, xor_1_out;

  not not_1 (not_1_out, a);
  and and_1 (and_1_out, not_1_out, b);
  xor xor_1 (xor_1_out, b, a);
  not not_2 (not_2_out, xor_1_out);
  and and_2 (and_2_out, not_2_out, carry_in);
  xor xor_2 (s, carry_in, xor_1_out);
  or or_1 (carry_out, and_2_out, and_1_out);

  // Notes on the sheet:
  //   Alvaro Henrique de Araujo Rungue - 395487
endmodule

module Exemplo0022 (
  input  in_1,
  input  in_2,
  input  in_3,
  input  in_4,
  input  in_5,
  input  in_6,
  input  in_7,
  input  in_8,
  input  in_9,
  output out_10,
  output out_11,
  output out_12,
  output out_13,
  output out_14
);

  wire fullsubtractor_1_carry_out, fullsubtractor_2_carry_out, fullsubtractor_3_carry_out;

  FullSubtractor fullsubtractor_1 (
    .carry_in(in_9), .carry_out(fullsubtractor_1_carry_out), .a(in_1), .b(in_2), .s(out_11));
  FullSubtractor fullsubtractor_2 (
    .carry_in(fullsubtractor_1_carry_out), .carry_out(fullsubtractor_2_carry_out), .a(in_3), .b(in_4),
    .s(out_12));
  FullSubtractor fullsubtractor_3 (
    .carry_in(fullsubtractor_2_carry_out), .carry_out(fullsubtractor_3_carry_out), .a(in_5), .b(in_6),
    .s(out_13));
  FullSubtractor fullsubtractor_4 (
    .carry_in(fullsubtractor_3_carry_out), .carry_out(out_10), .a(in_7), .b(in_8), .s(out_14));

  // Notes on the sheet:
  //   Alvaro Henrique de Araujo Rungue - 395487
endmodule
