// Logisim project Exemplo0023.circ as structural Verilog: 1 circuit, main circuit Exemplo23
module Exemplo23 (
  input  [3:0] in_1,
  input  [3:0] in_2,
  output [3:0] out_3
);

  xnor XNOR0 (out_3[0], in_1[0], in_2[0]);
  xnor XNOR1 (out_3[1], in_1[1], in_2[1]);
  xnor XNOR2 (out_3[2], in_1[2], in_2[2]);
  xnor XNOR3 (out_3[3], in_1[3], in_2[3]);

  // Notes on the sheet:
  //   Alvaro Henique de Araujo Rungue - 395487
endmodule
