// Logisim project Exemplo0024.circ as structural Verilog: 1 circuit, main circuit main
module main (
  input  [3:0] in_1,
  input  [3:0] in_2,
  output [3:0] out_3
);

  xor XOR0 (out_3[0], in_1[0], in_2[0]);
  xor XOR1 (out_3[1], in_1[1], in_2[1]);
  xor XOR2 (out_3[2], in_1[2], in_2[2]);
  xor XOR3 (out_3[3], in_1[3], in_2[3]);

  // Notes on the sheet:
  //   Alvaro Henique de Araujo Rungue - 395487
endmodule
