// Logisim project Exemplo0026.circ as structural Verilog: 2 circuits, main circuit FullAdder
// F.A
module FullAdder (
  input  a,
  input  b,
  input  carry_in,
  output carry_out,
  output s
);

  wire and_1_out, and_2_out, xor_1_out;

  xor xor_1 (xor_1_out, b, a);
  and and_1 (and_1_out, a, b);
  and and_2 (and_2_out, xor_1_out, carry_in);
  xor xor_2 (s, carry_in, xor_1_out);
  or or_1 (carry_out, and_2_out, and_1_out);

  // Notes on the sheet:
  //   Alvaro Henrique de Araujo Rungue - 395487
endmodule

module Exemplo0026 (
  input  a_3,
  input  b_3,
  input  a_2,
  input  b_2,
  input  a_1,
  input  b_1,
  input  a_0,
  input  b_0,
  input  Carry_in,
  output Carry_out,
  output s_3,
  output s_2,
  output s_1,
  output s_0
);

  wire fulladder_1_carry_out, fulladder_2_carry_out, fulladder_3_carry_out, fulladder_4_carry_out, xor_1_out,
       xor_2_out, xor_3_out, xor_4_out;

  xor xor_1 (xor_1_out, b_3, Carry_in);
  xor xor_2 (xor_2_out, b_2, Carry_in);
  FullAdder fulladder_1 (.carry_in(Carry_in), .a(a_3), .b(xor_1_out), .s(s_3), .carry_out(fulladder_1_carry_out));
  xor xor_3 (xor_3_out, b_1, Carry_in);
  FullAdder fulladder_2 (
    .carry_in(fulladder_3_carry_out), .a(a_1), .b(xor_3_out), .s(s_1), .carry_out(fulladder_2_carry_out));
  FullAdder fulladder_3 (
    .carry_in(fulladder_1_carry_out), .a(a_2), .b(xor_2_out), .s(s_2), .carry_out(fulladder_3_carry_out));
  xor xor_4 (xor_4_out, b_0, Carry_in);
  FullAdder fulladder_4 (
    .carry_in(fulladder_2_carry_out), .a(a_0), .b(xor_4_out), .s(s_0), .carry_out(fulladder_4_carry_out));
  xor xor_5 (Carry_out, Carry_in, fulladder_4_carry_out);

  // Notes on the sheet:
  //   Alvaro Henrique de Araujo Rungue - 395487
endmodule
