// Logisim project Exemplo0027.circ as structural Verilog: 3 circuits, main circuit Comparador
// C I
module Comparador (
  input  [3:0] in_1,
  input  [3:0] in_2,
  output [3:0] out_3
);

  xnor XNOR0 (out_3[0], in_1[0], in_2[0]);
  xnor XNOR1 (out_3[1], in_1[1], in_2[1]);
  xnor XNOR2 (out_3[2], in_1[2], in_2[2]);
  xnor XNOR3 (out_3[3], in_1[3], in_2[3]);

  // Notes on the sheet:
  //   Alvaro Henique de Araujo Rungue - 395487
endmodule

// C D
module ComparadorDiferenca (
  input  [3:0] in_1,
  input  [3:0] in_2,
  output [3:0] out_3
);

  xor XOR0 (out_3[0], in_1[0], in_2[0]);
  xor XOR1 (out_3[1], in_1[1], in_2[1]);
  xor XOR2 (out_3[2], in_1[2], in_2[2]);
  xor XOR3 (out_3[3], in_1[3], in_2[3]);

  // Notes on the sheet:
  //   Alvaro Henique de Araujo Rungue - 395487
endmodule

module Exemplo0027 (
  input  [3:0] a,
  input  [3:0] b,
  input  in_3,
  output [3:0] out_4
);

  wire undriven;
  wire [3:0] comparador_1_out_3, comparadordiferenca_1_out_3;

  Comparador comparador_1 (.in_1(a), .in_2(b), .out_3(comparador_1_out_3));
  Multiplexer #(.width(4)) multiplexer_1 (
    .in0(comparador_1_out_3), .in1(comparadordiferenca_1_out_3), .out(out_4), .sel(in_3), .en(undriven));
  ComparadorDiferenca comparadordiferenca_1 (.in_1(a), .in_2(b), .out_3(comparadordiferenca_1_out_3));

  // Notes on the sheet:
  //   Alvaro Henrique de Araujo Rungue - 395487
endmodule
