// Logisim project Circuitos.circ as structural Verilog: 11 circuits, main circuit FullAdder
// 4bit F.A
module Exemplo0021 (
  input  a_3,
  input  a_2,
  input  a_1,
  input  a_0,
  input  b_3,
  input  b_2,
  input  b_1,
  input  b_0,
  input  Carry_in,
  output Carry_out,
  output [3:0] out_11
);

  wire fulladder_1_carry_out, fulladder_2_carry_out, fulladder_3_carry_out;

  FullAdder fulladder_1 (.carry_in(Carry_in), .carry_out(fulladder_1_carry_out), .a(a_3), .b(b_3), .s(out_11[3]));
  FullAdder fulladder_2 (
    .carry_in(fulladder_1_carry_out), .carry_out(fulladder_2_carry_out), .a(a_2), .b(b_2), .s(out_11[2]));
  FullAdder fulladder_3 (
    .carry_in(fulladder_2_carry_out), .carry_out(fulladder_3_carry_out), .a(a_1), .b(b_1), .s(out_11[1]));
  FullAdder fulladder_4 (.carry_in(fulladder_3_carry_out), .carry_out(Carry_out), .a(a_0), .b(b_0), .s(out_11[0]));

  // Notes on the sheet:
  //   Exemplo0021 - Bruno Cezar Andrade Viallet - 396679
endmodule

module Exemplo0022 (
  input  a_3,
  input  a_2,
  input  a_1,
  input  a_0,
  input  b_3,
  input  b_2,
  input  b_1,
  input  b_0,
  input  Carry_in,
  output Carry_out,
  output [3:0] out_11
);

  wire fullsubtractor_1_carry_out, fullsubtractor_2_carry_out, fullsubtractor_3_carry_out;

  FullSubtractor fullsubtractor_1 (
    .carry_in(Carry_in), .a(a_3), .b(b_3), .s(out_11[0]), .carry_out(fullsubtractor_1_carry_out));
  FullSubtractor fullsubtractor_2 (
    .carry_in(fullsubtractor_3_carry_out), .a(a_1), .b(b_1), .s(out_11[2]),
    .carry_out(fullsubtractor_2_carry_out));
  FullSubtractor fullsubtractor_3 (
    .carry_in(fullsubtractor_1_carry_out), .a(a_2), .b(b_2), .s(out_11[1]),
    .carry_out(fullsubtractor_3_carry_out));
  FullSubtractor fullsubtractor_4 (
    .carry_in(fullsubtractor_2_carry_out), .a(a_0), .b(b_0), .s(out_11[3]), .carry_out(Carry_out));

  // Notes on the sheet:
  //   Exemplo0022 - Bruno Cezar Andrade Viallet - 396679
endmodule

// C I
module Exemplo0023 (
  input  [3:0] a,
  input  [3:0] b,
  output [3:0] out_3
);

  xnor _3 (out_3[3], a[3], b[3]);
  xnor _2 (out_3[2], a[2], b[2]);
  xnor _1 (out_3[1], a[1], b[1]);
  xnor _0 (out_3[0], a[0], b[0]);

  // Notes on the sheet:
  //   Exemplo0023 - Bruno Cezar Andrade Viallet - 396679
  //   Comparador de Igualdade
endmodule

module Exemplo0025 (
  input  [3:0] a,
  input  in_2,
  output out_3,
  output [3:0] Complemento_de_2
);

  wire [3:0] complemento_de_1_1_s;

  Complemento_de_1 complemento_de_1_1 (.a(a), .s(complemento_de_1_1_s));
  Exemplo0021 exemplo0021_1 (
    .Carry_in(in_2), .a_3(complemento_de_1_1_s[3]), .b_3(1'b0), .a_2(complemento_de_1_1_s[2]), .b_2(1'b0),
    .a_1(complemento_de_1_1_s[1]), .b_1(1'b0), .a_0(complemento_de_1_1_s[0]), .b_0(1'b1),
    .out_11(Complemento_de_2), .Carry_out(out_3));

  // Notes on the sheet:
  //   Exemplo0025 - Bruno Cezar Andrade Viallet - 396679
  //   Complemento de 1
endmodule

// C D
module Exemplo0024 (
  input  [3:0] a,
  input  [3:0] b,
  output [3:0] out_3
);

  xor _4 (out_3[3], a[3], b[3]);
  xor _3 (out_3[2], a[2], b[2]);
  xor _2 (out_3[1], a[1], b[1]);
  xor _1 (out_3[0], a[0], b[0]);

  // Notes on the sheet:
  //   Exemplo0024 - Bruno Cezar Andrade Viallet - 396679
  //   Comparador de Diferença
endmodule

module Exemplo0026 (
  input  a_3,
  input  a_2,
  input  a_1,
  input  a_0,
  input  b_3,
  input  b_2,
  input  b_1,
  input  b_0,
  input  Carry_in,
  output Carry_out,
  output [3:0] out_11
);

  wire fulladder_1_carry_out, fulladder_2_carry_out, fulladder_3_carry_out, fulladder_4_carry_out, xor_1_out,
       xor_2_out, xor_3_out, xor_4_out;

  xor xor_1 (xor_1_out, b_3, Carry_in);
  xor xor_2 (xor_2_out, b_2, Carry_in);
  FullAdder fulladder_1 (.carry_in(Carry_in), .carry_out(fulladder_1_carry_out), .a(a_3), .b(xor_1_out), .s(out_11[3]));
  xor xor_3 (xor_3_out, b_1, Carry_in);
  FullAdder fulladder_2 (
    .carry_in(fulladder_3_carry_out), .carry_out(fulladder_2_carry_out), .a(a_1), .b(xor_3_out), .s(out_11[1]));
  FullAdder fulladder_3 (
    .carry_in(fulladder_1_carry_out), .carry_out(fulladder_3_carry_out), .a(a_2), .b(xor_2_out), .s(out_11[2]));
  xor xor_4 (xor_4_out, b_0, Carry_in);
  FullAdder fulladder_4 (
    .carry_in(fulladder_2_carry_out), .carry_out(fulladder_4_carry_out), .a(a_0), .b(xor_4_out), .s(out_11[0]));
  xor xor_5 (Carry_out, Carry_in, fulladder_4_carry_out);

  // Notes on the sheet:
  //   Exemplo0026 - Bruno Cezar Andrade Viallet - 396679
endmodule

module Exemplo0027 (
  input  [3:0] a,
  input  [3:0] b,
  input  in_3,
  output [3:0] out_4
);

  wire undriven;
  wire [3:0] exemplo0023_1_out_3, exemplo0024_1_out_3;

  Exemplo0023 exemplo0023_1 (.a(a), .out_3(exemplo0023_1_out_3), .b(b));
  Multiplexer #(.width(4)) multiplexer_1 (
    .in0(exemplo0023_1_out_3), .in1(exemplo0024_1_out_3), .out(out_4), .sel(in_3), .en(undriven));
  Exemplo0024 exemplo0024_1 (.a(a), .out_3(exemplo0024_1_out_3), .b(b));

  // Notes on the sheet:
  //   Exemplo0027 - Bruno Cezar Andrade Viallet - 396679
endmodule

// F.S
module FullSubtractor (
  input  a,
  input  b,
  input  carry_in,
  output carry_out,
  output s
);

  wire and_1_out, and_2_out, not_1_out, not_2_out, xor_1_out;

  not not_1 (not_1_out, a);
  xor xor_1 (xor_1_out, b, a);
  and and_1 (and_1_out, not_1_out, b);
  not not_2 (not_2_out, xor_1_out);
  and and_2 (and_2_out, not_2_out, carry_in);
  xor xor_2 (s, carry_in, xor_1_out);
  or or_1 (carry_out, and_2_out, and_1_out);

  // Notes on the sheet:
  //   Bruno Cezar Andrade Viallet - 396679
endmodule

// F.A
module FullAdder (
  input  a,
  input  b,
  input  carry_in,
  output carry_out,
  output s
);

  wire and_1_out, and_2_out, xor_1_out;

  xor xor_1 (xor_1_out, b, a);
  and and_1 (and_1_out, a, b);
  and and_2 (and_2_out, xor_1_out, carry_in);
  xor xor_2 (s, carry_in, xor_1_out);
  or or_1 (carry_out, and_2_out, and_1_out);

  // Notes on the sheet:
  //   Bruno Cezar Andrade Viallet - 396679
endmodule

// C 1
module Complemento_de_1 (
  input  [3:0] a,
  output [3:0] s
);

  assign s = ~a;  // NOT_Gate not_1, 4 bits wide

  // Notes on the sheet:
  //   Bruno Cezar Andrade Viallet - 396679
endmodule

module circuit (
  input  in_1,
  input  in_2,
  input  in_3,
  input  in_4,
  input  in_5,
  input  in_6,
  input  in_7,
  input  in_8,
  input  in_9,
  output out_10
);

  wire nand_1_out, nand_2_out, nand_3_out, not_1_out, not_2_out, not_3_out, not_4_out, not_5_out, not_7_out,
       not_8_out, not_9_out, not_10_out, xnor_1_out, xnor_2_out, xnor_3_out, xnor_4_out;

  not not_1 (not_1_out, in_2);
  not not_2 (not_2_out, in_4);
  not not_3 (not_3_out, in_7);
  not not_4 (not_4_out, in_9);
  xnor xnor_1 (xnor_1_out, not_1_out, not_2_out);
  xnor xnor_2 (xnor_2_out, not_3_out, not_4_out);
  nand nand_1 (nand_1_out, xnor_1_out, xnor_2_out);
  not not_5 (not_5_out, in_1);
  nand nand_2 (nand_2_out, xnor_3_out, xnor_4_out);
  nand nand_3 (nand_3_out, nand_1_out, not_5_out, nand_2_out);
  not not_6 (out_10, nand_3_out);
  xnor xnor_3 (xnor_3_out, not_7_out, not_8_out);
  xnor xnor_4 (xnor_4_out, not_9_out, not_10_out);
  not not_7 (not_7_out, in_3);
  not not_8 (not_8_out, in_5);
  not not_9 (not_9_out, in_6);
  not not_10 (not_10_out, in_8);
endmodule
