// Logisim project Exemplo21.circ as structural Verilog: 2 circuits, main circuit Soma
module Soma (
  input  a,
  input  b,
  input  Carry_in,
  output \output ,
  output Carry_on
);

  wire and_1_out, and_2_out, xor_1_out;

  xor xor_1 (xor_1_out, b, a);
  and and_1 (and_1_out, b, a);
  xor xor_2 (\output , xor_1_out, Carry_in);
  and and_2 (and_2_out, xor_1_out, Carry_in);
  or or_1 (Carry_on, and_2_out, and_1_out);
endmodule

module Soma_4bits (
  input  in_1,
  input  in_2,
  input  in_3,
  input  in_4,
  input  in_5,
  input  in_6,
  input  in_7,
  input  in_8,
  input  carry_In,
  output out_10,
  output out_11,
  output out_12,
  output out_13,
  output out_14
);

  wire soma_1_carry_on, soma_2_carry_on, soma_3_carry_on;

  Soma soma_1 (.Carry_in(carry_In), .a(in_4), .b(in_8), .\output (out_14), .Carry_on(soma_1_carry_on));
  Soma soma_2 (.Carry_in(soma_1_carry_on), .a(in_3), .b(in_7), .\output (out_13), .Carry_on(soma_2_carry_on));
  Soma soma_3 (.Carry_in(soma_2_carry_on), .a(in_2), .b(in_6), .\output (out_12), .Carry_on(soma_3_carry_on));
  Soma soma_4 (.Carry_in(soma_3_carry_on), .a(in_1), .b(in_5), .\output (out_11), .Carry_on(out_10));
endmodule
