// Logisim project Exemplo22.circ as structural Verilog: 1 circuit, main circuit Subtractor
module Subtractor (
  input  [3:0] a,
  input  [3:0] b,
  input  [3:0] carry_in,
  output [3:0] saida,
  output carry_on
);

  wire [3:0] a_xor_b_out, n_a___b_out, n_a_xor_b_____carry_in_out, n_a_xor_b_out, na_out;
  wire [3:1] n_a_b__xor___a_xor_b_____carry_in_out;

  assign na_out = ~a;  // NOT_Gate na, 4 bits wide
  assign a_xor_b_out = a ^ b;  // XOR_Gate a_xor_b, 4 bits wide
  assign n_a___b_out = na_out & b;  // AND_Gate n_a___b, 4 bits wide
  assign n_a_xor_b_out = ~a_xor_b_out;  // NOT_Gate n_a_xor_b, 4 bits wide
  assign saida = a_xor_b_out ^ carry_in;  // XOR_Gate a_xor_b__xor__carry_in, 4 bits wide
  assign n_a_xor_b_____carry_in_out = n_a_xor_b_out & carry_in;  // AND_Gate n_a_xor_b_____carry_in, 4 bits wide
  assign {n_a_b__xor___a_xor_b_____carry_in_out, carry_on} = ~(n_a___b_out ^ n_a_xor_b_____carry_in_out);  // XNOR_Gate n_a_b__xor___a_xor_b_____carry_in, 4 bits wide
endmodule
