// Logisim project Exemplo23.circ as structural Verilog: 1 circuit, main circuit Equality
module Equality (
  input  [3:0] in_1,
  input  [3:0] in_2,
  output [3:0] out_3,
  output out_4
);

  assign out_3 = ~(in_1 ^ in_2);  // XNOR_Gate xnor_1, 4 bits wide
  and and_1 (out_4, out_3[0], out_3[1], out_3[2], out_3[3]);

  // Notes on the sheet:
  //   Circuito equality
  //   resultado 1=equality
endmodule
