// Logisim project Exemplo25.circ as structural Verilog: 2 circuits, main circuit Complemento de 2
module Complemento_de_2 (
  input  [3:0] ENTRADA,
  input  SOMA_1,
  input  in_3,
  output [4:0] out_4
);

  wire soma_1_out_5, soma_2_out_5, soma_3_out_5;
  wire [3:0] not_1_out;

  assign not_1_out = ~ENTRADA;  // NOT_Gate not_1, 4 bits wide
  Soma u_soma_1 (.entrada_overflow(in_3), .a(not_1_out[3]), .b(SOMA_1), .\output (out_4[3]), .out_5(soma_1_out_5));
  Soma soma_2 (
    .entrada_overflow(soma_1_out_5), .a(not_1_out[2]), .b(SOMA_1), .\output (out_4[2]), .out_5(soma_2_out_5));
  Soma soma_3 (
    .entrada_overflow(soma_2_out_5), .a(not_1_out[1]), .b(SOMA_1), .\output (out_4[1]), .out_5(soma_3_out_5));
  Soma soma_4 (.entrada_overflow(soma_3_out_5), .a(not_1_out[0]), .b(SOMA_1), .\output (out_4[0]), .out_5(out_4[4]));

  // Notes on the sheet:
  //   COMPLEMENTO DE 2
  //   resultado complemento de 2
endmodule

module Soma (
  input  a,
  input  b,
  input  entrada_overflow,
  output \output ,
  output out_5
);

  wire and_1_out, and_2_out, xor_1_out;

  xor xor_1 (xor_1_out, b, a);
  and and_1 (and_1_out, b, a);
  xor xor_2 (\output , xor_1_out, entrada_overflow);
  and and_2 (and_2_out, xor_1_out, entrada_overflow);
  or or_1 (out_5, and_2_out, and_1_out);
endmodule
