// Logisim project Exemplo0021.circ as structural Verilog: 4 circuits, main circuit main
module main (
  input  [3:0] in_1,
  input  [3:0] in_2,
  output [4:0] out_3
);

  fullAdder4 fulladder4_1 (.in_1(in_1), .in_2(in_2), .out_3(out_3));
endmodule

// FA
module fullAdder (
  input  a,
  input  b,
  input  c,
  output s1,
  output s0
);

  wire and_1_out, and_2_out, xor_1_out;

  xor xor_1 (xor_1_out, b, a);
  and and_1 (and_1_out, b, a);
  xor xor_2 (s1, c, xor_1_out);
  and and_2 (and_2_out, xor_1_out, c);
  or or_1 (s0, and_2_out, and_1_out);
endmodule

// HA
module halfAdder (
  input  in_1,
  input  in_2,
  output s1,
  output s0
);

  xor xor_1 (s1, in_2, in_1);
  and and_1 (s0, in_2, in_1);
endmodule

// FA4
module fullAdder4 (
  input  [3:0] in_1,
  input  [3:0] in_2,
  output [4:0] out_3
);

  wire fulladder_1_s0, fulladder_2_s0, halfadder_1_s0;

  halfAdder halfadder_1 (.in_1(in_1[0]), .in_2(in_2[0]), .s0(halfadder_1_s0), .s1(out_3[0]));
  fullAdder fulladder_1 (.a(in_1[1]), .b(in_2[1]), .c(halfadder_1_s0), .s0(fulladder_1_s0), .s1(out_3[1]));
  fullAdder fulladder_2 (.a(in_2[2]), .b(in_1[2]), .c(fulladder_1_s0), .s0(fulladder_2_s0), .s1(out_3[2]));
  fullAdder fulladder_3 (.a(in_2[3]), .b(in_1[3]), .c(fulladder_2_s0), .s0(out_3[4]), .s1(out_3[3]));
endmodule
