// Logisim project Exemplo0023.circ as structural Verilog: 2 circuits, main circuit main
module main (
  input  [3:0] in_1,
  input  [3:0] in_2,
  output [3:0] out_3
);

  comparadorIgualdade comparadorigualdade_1 (.in_1(in_1), .in_2(in_2), .out_3(out_3));
endmodule

// CI
module comparadorIgualdade (
  input  [3:0] in_1,
  input  [3:0] in_2,
  output [3:0] out_3
);

  xnor xnor_1 (out_3[0], in_1[0], in_2[0]);
  xnor xnor_2 (out_3[1], in_1[1], in_2[1]);
  xnor xnor_3 (out_3[2], in_1[2], in_2[2]);
  xnor xnor_4 (out_3[3], in_1[3], in_2[3]);
endmodule
