// Logisim project Exemplo0025.circ as structural Verilog: 3 circuits, main circuit main
module main (
  input  [3:0] in_1,
  output [3:0] out_2
);

  complemeto2 complemeto2_1 (.in_1(in_1), .out_2(out_2));
endmodule

// HA
module halfAdder (
  input  in_1,
  input  in_2,
  output out_3,
  output out_4
);

  xor xor_1 (out_3, in_2, in_1);
  and and_1 (out_4, in_2, in_1);
endmodule

// C2
module complemeto2 (
  input  [3:0] in_1,
  output [3:0] out_2
);

  wire halfadder_1_out_4, halfadder_2_out_4, halfadder_3_out_4;
  wire [3:0] not_1_out;

  assign not_1_out = ~in_1;  // NOT_Gate not_1, 4 bits wide
  halfAdder halfadder_1 (.in_1(1'b1), .in_2(not_1_out[0]), .out_4(halfadder_1_out_4), .out_3(out_2[0]));
  halfAdder halfadder_2 (.in_1(halfadder_1_out_4), .in_2(not_1_out[1]), .out_4(halfadder_2_out_4), .out_3(out_2[1]));
  halfAdder halfadder_3 (.in_1(halfadder_2_out_4), .in_2(not_1_out[2]), .out_4(halfadder_3_out_4), .out_3(out_2[2]));
  halfAdder halfadder_4 (.in_1(halfadder_3_out_4), .in_2(not_1_out[3]), .out_3(out_2[3]));  // open: out_4
endmodule
