// Logisim project Exemplo0026.circ as structural Verilog: 6 circuits, main circuit main
module main (
  input  [3:0] in_1,
  input  [3:0] in_2,
  input  in_3,
  output [3:0] out_4,
  output out_5
);

  SumSub sumsub_1 (.in_1(in_1), .in_2(in_2), .in_3(in_3), .out_4(out_4), .out_5(out_5));

  // Notes on the sheet:
  //   bit usado quando o resultado da soma tiver 5 bits (sinal=1+amplitude=4)
endmodule

// HA
module halfAdder (
  input  in_1,
  input  in_2,
  output out_3,
  output out_4
);

  xor xor_1 (out_3, in_2, in_1);
  and and_1 (out_4, in_2, in_1);
endmodule

// C2
module complemeto2 (
  input  [3:0] in_1,
  output [3:0] out_2,
  output out_3
);

  wire halfadder_1_out_4, halfadder_2_out_4, halfadder_3_out_4;
  wire [3:0] not_1_out;

  assign not_1_out = ~in_1;  // NOT_Gate not_1, 4 bits wide
  halfAdder halfadder_1 (.in_1(1'b1), .in_2(not_1_out[0]), .out_4(halfadder_1_out_4), .out_3(out_2[0]));
  halfAdder halfadder_2 (.in_1(halfadder_1_out_4), .in_2(not_1_out[1]), .out_4(halfadder_2_out_4), .out_3(out_2[1]));
  halfAdder halfadder_3 (.in_1(halfadder_2_out_4), .in_2(not_1_out[2]), .out_4(halfadder_3_out_4), .out_3(out_2[2]));
  halfAdder halfadder_4 (.in_1(halfadder_3_out_4), .in_2(not_1_out[3]), .out_4(out_3), .out_3(out_2[3]));
endmodule

// FA
module fullAdder (
  input  in_1,
  input  in_2,
  input  in_3,
  output out_4,
  output out_5
);

  wire and_1_out, and_2_out, xor_1_out;

  xor xor_1 (xor_1_out, in_2, in_1);
  and and_1 (and_1_out, in_2, in_1);
  xor xor_2 (out_4, in_3, xor_1_out);
  and and_2 (and_2_out, xor_1_out, in_3);
  or or_1 (out_5, and_2_out, and_1_out);
endmodule

// FA4
module fullAdder4 (
  input  [3:0] in_1,
  input  [3:0] in_2,
  output [4:0] out_3
);

  wire fulladder_1_out_5, fulladder_2_out_5, halfadder_1_out_4;

  halfAdder halfadder_1 (.in_1(in_1[0]), .in_2(in_2[0]), .out_4(halfadder_1_out_4), .out_3(out_3[0]));
  fullAdder fulladder_1 (
    .in_1(in_1[1]), .in_2(in_2[1]), .in_3(halfadder_1_out_4), .out_5(fulladder_1_out_5), .out_4(out_3[1]));
  fullAdder fulladder_2 (
    .in_1(in_1[2]), .in_2(in_2[2]), .in_3(fulladder_1_out_5), .out_5(fulladder_2_out_5), .out_4(out_3[2]));
  fullAdder fulladder_3 (.in_1(in_1[3]), .in_2(in_2[3]), .in_3(fulladder_2_out_5), .out_5(out_3[4]), .out_4(out_3[3]));
endmodule

// +/-
module SumSub (
  input  [3:0] in_1,
  input  [3:0] in_2,
  input  in_3,
  output [3:0] out_4,
  output out_5
);

  wire complemeto2_1_out_3;
  wire [3:0] complemeto2_1_out_2, multiplexer_1_out;
  wire [4:4] fulladder4_1_out_3;

  complemeto2 complemeto2_1 (.in_1(in_2), .out_3(complemeto2_1_out_3), .out_2(complemeto2_1_out_2));
  fullAdder4 fulladder4_1 (.in_1(in_1), .in_2(multiplexer_1_out), .out_3({fulladder4_1_out_3[4], out_4}));
  Multiplexer #(.width(4), .enable("false")) multiplexer_1 (
    .in0(in_2), .in1(complemeto2_1_out_2), .out(multiplexer_1_out), .sel(in_3));
  Multiplexer #(.enable("false")) multiplexer_2 (
    .in0(fulladder4_1_out_3[4]), .in1(complemeto2_1_out_3), .out(out_5), .sel(in_3));
endmodule
