// Logisim project Exemplo0027.circ as structural Verilog: 4 circuits, main circuit main
module main (
  input  [3:0] in_1,
  input  [3:0] in_2,
  input  in_3,
  output [3:0] out_4
);

  compIgualDifer compigualdifer_1 (.in_1(in_1), .in_2(in_2), ._0___Igualdade(in_3), .out_4(out_4));
endmodule

// CI
module comparadorIgualdade (
  input  [3:0] in_1,
  input  [3:0] in_2,
  output [3:0] out_3
);

  xnor xnor_1 (out_3[0], in_1[0], in_2[0]);
  xnor xnor_2 (out_3[1], in_1[1], in_2[1]);
  xnor xnor_3 (out_3[2], in_1[2], in_2[2]);
  xnor xnor_4 (out_3[3], in_1[3], in_2[3]);
endmodule

// CD
module comparadorDiferenca (
  input  [3:0] in_1,
  input  [3:0] in_2,
  output [3:0] out_3
);

  xor xor_1 (out_3[0], in_1[0], in_2[0]);
  xor xor_2 (out_3[1], in_1[1], in_2[1]);
  xor xor_3 (out_3[2], in_1[2], in_2[2]);
  xor xor_4 (out_3[3], in_1[3], in_2[3]);
endmodule

// CID
module compIgualDifer (
  input  [3:0] in_1,
  input  [3:0] in_2,
  input  _0___Igualdade,
  output [3:0] out_4
);

  wire [3:0] comparadordiferenca_1_out_3, comparadorigualdade_1_out_3;

  comparadorIgualdade comparadorigualdade_1 (.in_1(in_1), .in_2(in_2), .out_3(comparadorigualdade_1_out_3));
  Multiplexer #(.width(4), .enable("false")) multiplexer_1 (
    .in0(comparadorigualdade_1_out_3), .in1(comparadordiferenca_1_out_3), .out(out_4), .sel(_0___Igualdade));
  comparadorDiferenca comparadordiferenca_1 (.in_1(in_1), .in_2(in_2), .out_3(comparadordiferenca_1_out_3));

  // Notes on the sheet:
  //   1 - Diferenca
endmodule
