// Logisim project Exemplo0022.circ as structural Verilog: 4 circuits, main circuit main
module main (
  input  Carry_in,
  input  [3:0] a,
  input  [3:0] b,
  output [3:0] S,
  output Carry_out
);

  \diferença_completa2  \diferença_completa2_1  (.a(a), .b(b), .Carry_in(Carry_in), .Carry_out(Carry_out), .S(S));
endmodule

// MD
module \meia_diferença  (
  input  a,
  input  b,
  output s,
  output Carry_out
);

  wire not_1_out;

  not not_1 (not_1_out, a);
  xor xor_1 (s, a, b);
  and and_1 (Carry_out, not_1_out, b);
endmodule

// DC
module \diferença_completa  (
  input  Carry_in,
  input  a,
  input  b,
  output S,
  output Carry_out
);

  wire \meia_diferença_1_carry_out , \meia_diferença_1_s , \meia_diferença_2_carry_out ;

  \meia_diferença  \meia_diferença_1  (
    .a(a), .b(b), .s(\meia_diferença_1_s ), .Carry_out(\meia_diferença_1_carry_out ));
  \meia_diferença  \meia_diferença_2  (
    .a(\meia_diferença_1_s ), .b(Carry_in), .s(S), .Carry_out(\meia_diferença_2_carry_out ));
  or or_1 (Carry_out, \meia_diferença_1_carry_out , \meia_diferença_2_carry_out );
endmodule

// DC2
module \diferença_completa2  (
  input  [3:0] a,
  input  [3:0] b,
  input  Carry_in,
  output [3:0] S,
  output Carry_out
);

  wire \diferença_completa_1_carry_out , \diferença_completa_2_carry_out , \diferença_completa_3_carry_out ;

  \diferença_completa  \diferença_completa_1  (
    .a(a[0]), .b(b[0]), .Carry_in(Carry_in), .Carry_out(\diferença_completa_1_carry_out ), .S(S[0]));
  \diferença_completa  \diferença_completa_2  (
    .a(a[1]), .b(b[1]), .Carry_in(\diferença_completa_1_carry_out ),
    .Carry_out(\diferença_completa_2_carry_out ), .S(S[1]));
  \diferença_completa  \diferença_completa_3  (
    .a(a[2]), .b(b[2]), .Carry_in(\diferença_completa_2_carry_out ),
    .Carry_out(\diferença_completa_3_carry_out ), .S(S[2]));
  \diferença_completa  \diferença_completa_4  (
    .a(a[3]), .b(b[3]), .Carry_in(\diferença_completa_3_carry_out ), .Carry_out(Carry_out), .S(S[3]));
endmodule
