// Logisim project Exemplo0024.circ as structural Verilog: 3 circuits, main circuit main
module main (
  input  [3:0] a,
  input  [3:0] b,
  output S
);

  \Diferença2  \diferença2_1  (.a(a), .b(b), .S(S));
endmodule

// =!
module \Diferença  (
  input  a,
  input  b,
  output s
);

  xor xor_1 (s, a, b);
endmodule

// =!
module \Diferença2  (
  input  [3:0] a,
  input  [3:0] b,
  output S
);

  wire \diferença_1_s , \diferença_2_s , \diferença_3_s , \diferença_4_s ;

  \Diferença  \diferença_1  (.a(a[0]), .b(b[0]), .s(\diferença_1_s ));
  \Diferença  \diferença_2  (.a(a[1]), .b(b[1]), .s(\diferença_2_s ));
  \Diferença  \diferença_3  (.a(a[2]), .b(b[2]), .s(\diferença_3_s ));
  \Diferença  \diferença_4  (.a(a[3]), .b(b[3]), .s(\diferença_4_s ));
  or or_1 (S, \diferença_1_s , \diferença_2_s , \diferença_3_s , \diferença_4_s );
endmodule
