// Logisim project Exemplo0025.circ as structural Verilog: 4 circuits, main circuit main
module main (
  input  [3:0] a,
  output [3:0] s,
  output Carry_out
);

  Complemento_de_2 complemento_de_2_1 (.a(a), .Carry_out(Carry_out), .s(s));
endmodule

// C1
module Complemento_de_1 (
  input  a,
  output s
);

  not not_1 (s, a);
endmodule

// HA
module halfAdder (
  input  a,
  input  b,
  output s,
  output Carry_out
);

  xor xor_1 (s, a, b);
  and and_1 (Carry_out, a, b);
endmodule

// C2
module Complemento_de_2 (
  input  [3:0] a,
  output [3:0] s,
  output Carry_out
);

  wire complemento_de_1_1_s, complemento_de_1_2_s, complemento_de_1_3_s, complemento_de_1_4_s,
       halfadder_1_carry_out, halfadder_2_carry_out, halfadder_3_carry_out;

  Complemento_de_1 complemento_de_1_1 (.a(a[0]), .s(complemento_de_1_1_s));
  Complemento_de_1 complemento_de_1_2 (.a(a[1]), .s(complemento_de_1_2_s));
  Complemento_de_1 complemento_de_1_3 (.a(a[2]), .s(complemento_de_1_3_s));
  Complemento_de_1 complemento_de_1_4 (.a(a[3]), .s(complemento_de_1_4_s));
  halfAdder halfadder_1 (.b(complemento_de_1_1_s), .a(1'b1), .Carry_out(halfadder_1_carry_out), .s(s[0]));
  halfAdder halfadder_2 (
    .b(complemento_de_1_2_s), .a(halfadder_1_carry_out), .Carry_out(halfadder_2_carry_out), .s(s[1]));
  halfAdder halfadder_3 (
    .b(complemento_de_1_3_s), .a(halfadder_2_carry_out), .Carry_out(halfadder_3_carry_out), .s(s[2]));
  halfAdder halfadder_4 (.b(complemento_de_1_4_s), .a(halfadder_3_carry_out), .Carry_out(Carry_out), .s(s[3]));
endmodule
