// Logisim project Exemplo0027.circ as structural Verilog: 1 circuit, main circuit main
module main (
  input  [3:0] a,
  input  [3:0] b,
  input  chave,
  output [3:0] S
);

  wire [3:0] and_1_out, and_2_out, not_1_out, xnor_1_out, xor_1_out;

  assign xor_1_out = a ^ b;  // XOR_Gate xor_1, 4 bits wide
  assign xnor_1_out = ~(a ^ b);  // XNOR_Gate xnor_1, 4 bits wide
  assign not_1_out = ~{4{chave}};  // NOT_Gate not_1, 4 bits wide
  assign and_1_out = xor_1_out & {4{chave}};  // AND_Gate and_1, 4 bits wide
  assign and_2_out = xnor_1_out & not_1_out;  // AND_Gate and_2, 4 bits wide
  assign S = and_1_out | and_2_out;  // OR_Gate or_1, 4 bits wide
endmodule
