// Logisim project Exercicios.circ as structural Verilog
module meia_soma (
  input  A,
  input  B,
  output Q0,
  output Q1
);

  xor xor_1 (Q0, A, B);
  and and_1 (Q1, B, A);
endmodule

module soma_completa (
  input  Vai_um,
  input  A,
  input  B,
  output Q0,
  output Q1
);

  wire meia_soma_1_q1, meia_soma_2_q0, meia_soma_2_q1;

  meia_soma meia_soma_1 (.A(Vai_um), .B(meia_soma_2_q0), .Q0(Q0), .Q1(meia_soma_1_q1));
  meia_soma meia_soma_2 (.A(A), .B(B), .Q0(meia_soma_2_q0), .Q1(meia_soma_2_q1));
  or or_1 (Q1, meia_soma_1_q1, meia_soma_2_q1);
endmodule

module sub_completa (
  input  Vem_Um,
  input  A,
  input  B,
  output Q0,
  output Q1
);

  wire meia_sub_1_s0, meia_sub_1_s1, meia_sub_2_s1;

  meia_sub meia_sub_1 (.B(B), .A(A), .S0(meia_sub_1_s0), .S1(meia_sub_1_s1));
  meia_sub meia_sub_2 (.B(Vem_Um), .A(meia_sub_1_s0), .S0(Q0), .S1(meia_sub_2_s1));
  or or_1 (Q1, meia_sub_2_s1, meia_sub_1_s1);
endmodule

module meia_sub (
  input  B,
  input  A,
  output S0,
  output S1
);

  wire not_1_out;

  not not_1 (not_1_out, A);
  xor xor_1 (S0, B, A);
  and and_1 (S1, not_1_out, B);
endmodule

module Soma_4bits (
  input  a0,
  input  a1,
  input  a2,
  input  a3,
  input  b0,
  input  b1,
  input  b2,
  input  b3,
  output s0,
  output s1,
  output s2,
  output s3,
  output carry_out
);

  wire meia_soma_1_q1, soma_completa_1_q1, soma_completa_2_q1;

  meia_soma meia_soma_1 (.A(a0), .B(b0), .Q0(s0), .Q1(meia_soma_1_q1));
  soma_completa soma_completa_1 (.Vai_um(a1), .A(b1), .B(meia_soma_1_q1), .Q0(s1), .Q1(soma_completa_1_q1));
  soma_completa soma_completa_2 (.Vai_um(a2), .A(b2), .B(soma_completa_1_q1), .Q0(s2), .Q1(soma_completa_2_q1));
  soma_completa soma_completa_3 (.Vai_um(a3), .A(b3), .B(soma_completa_2_q1), .Q0(s3), .Q1(carry_out));
endmodule

module Sub_4bits (
  input  a0,
  input  a1,
  input  a2,
  input  a3,
  input  b0,
  input  b1,
  input  b2,
  input  b3,
  output s0,
  output s1,
  output s2,
  output s3,
  output carry_out
);

  wire meia_sub_1_s1, sub_completa_1_q1, sub_completa_2_q1;

  meia_sub meia_sub_1 (.B(a0), .A(b0), .S0(s0), .S1(meia_sub_1_s1));
  sub_completa sub_completa_1 (.Vem_Um(a1), .A(b1), .B(meia_sub_1_s1), .Q0(s1), .Q1(sub_completa_1_q1));
  sub_completa sub_completa_2 (.Vem_Um(a2), .A(b2), .B(sub_completa_1_q1), .Q0(s2), .Q1(sub_completa_2_q1));
  sub_completa sub_completa_3 (.Vem_Um(a3), .A(b3), .B(sub_completa_2_q1), .Q0(s3), .Q1(carry_out));
endmodule

module comparador_bits_iguais (
  input  a0,
  input  a1,
  input  a2,
  input  a3,
  input  b0,
  input  b1,
  input  b2,
  input  b3,
  output out_9
);

  wire xnor_1_out, xnor_2_out, xnor_3_out, xnor_4_out;

  xnor xnor_1 (xnor_1_out, a0, b0);
  xnor xnor_2 (xnor_2_out, a1, b1);
  xnor xnor_3 (xnor_3_out, a2, b2);
  xnor xnor_4 (xnor_4_out, a3, b3);
  and and_1 (out_9, xnor_1_out, xnor_2_out, xnor_3_out, xnor_4_out);
endmodule

module \comparador_bits_diferença  (
  input  a0,
  input  a1,
  input  a2,
  input  a3,
  input  b0,
  input  b1,
  input  b2,
  input  b3,
  output out_9
);

  wire and_1_out, xnor_1_out, xnor_2_out, xnor_3_out, xnor_4_out;

  xnor xnor_1 (xnor_1_out, a0, b0);
  xnor xnor_2 (xnor_2_out, a1, b1);
  xnor xnor_3 (xnor_3_out, a2, b2);
  xnor xnor_4 (xnor_4_out, a3, b3);
  and and_1 (and_1_out, xnor_1_out, xnor_2_out, xnor_3_out, xnor_4_out);
  not not_1 (out_9, and_1_out);
endmodule

module complemento_2 (
  input  a0,
  input  a1,
  input  a2,
  input  a3,
  output s0,
  output s1,
  output s2,
  output s3,
  output carry_out
);

  wire complemento_1_1_s0, complemento_1_1_s1, complemento_1_1_s2, complemento_1_1_s3;

  complemento_1 complemento_1_1 (
    .a0(a0), .a1(a1), .a2(a2), .a3(a3), .s0(complemento_1_1_s0), .s1(complemento_1_1_s1),
    .s2(complemento_1_1_s2), .s3(complemento_1_1_s3));
  Soma_4bits soma_4bits_1 (
    .a0(complemento_1_1_s3), .a1(complemento_1_1_s2), .a2(complemento_1_1_s1), .a3(complemento_1_1_s0),
    .b0(1'b1), .b1(1'b0), .b2(1'b0), .b3(1'b0), .s0(s0), .s1(s1), .s2(s2), .s3(s3), .carry_out(carry_out));
endmodule

module complemento_1 (
  input  a0,
  input  a1,
  input  a2,
  input  a3,
  output s0,
  output s1,
  output s2,
  output s3
);

  not not_1 (s0, a0);
  not not_2 (s1, a1);
  not not_3 (s2, a2);
  not not_4 (s3, a3);
endmodule
