// Logisim project Exemplo0021_logisim.circ as structural Verilog: 4 circuits, main circuit main
module main (
  input  a3,
  input  a2,
  input  a1,
  input  a0,
  input  zero,
  input  b3,
  input  b2,
  input  b1,
  input  b0,
  output out_10,
  output out_11,
  output out_12,
  output out_13,
  output out_14
);

  _4bitAdder u_4bitadder_1 (
    .a3(a3), .a2(a2), .a1(a1), .a0(a0), .zero(zero), .b3(b3), .b2(b2), .b1(b1), .b0(b0), .s0(out_13),
    .s1(out_12), .s2(out_11), .s3(out_10), .carry(out_14));

  // Notes on the sheet:
  //   Não sei como usar uma constante, mas a entrada com rótulo "zero" deve ser sempre igual a 0.
endmodule

module halfAdder (
  input  a,
  input  b,
  output s,
  output c
);

  xor xor_1 (s, a, b);
  and and_1 (c, a, b);
endmodule

module fullAdder (
  input  a,
  input  b,
  input  c,
  output s0,
  output s1
);

  wire halfadder_1_c, halfadder_1_s, halfadder_2_c;

  halfAdder halfadder_1 (.a(a), .b(b), .s(halfadder_1_s), .c(halfadder_1_c));
  halfAdder halfadder_2 (.a(halfadder_1_s), .b(c), .s(s0), .c(halfadder_2_c));
  or or_1 (s1, halfadder_2_c, halfadder_1_c);
endmodule

module _4bitAdder (
  input  a3,
  input  a2,
  input  a1,
  input  a0,
  input  zero,
  input  b3,
  input  b2,
  input  b1,
  input  b0,
  output s0,
  output s1,
  output s2,
  output s3,
  output carry
);

  wire fulladder_1_s1, fulladder_2_s1, fulladder_3_s1;

  fullAdder fulladder_1 (.a(a0), .b(b0), .c(zero), .s0(s0), .s1(fulladder_1_s1));
  fullAdder fulladder_2 (.a(a1), .b(b1), .c(fulladder_1_s1), .s0(s1), .s1(fulladder_2_s1));
  fullAdder fulladder_3 (.a(a2), .b(b2), .c(fulladder_2_s1), .s0(s2), .s1(fulladder_3_s1));
  fullAdder fulladder_4 (.a(a3), .b(b3), .c(fulladder_3_s1), .s0(s3), .s1(carry));

  // Notes on the sheet:
  //   Não sei como usar uma constante, mas a entrada com rótulo "zero" deve ser sempre igual a 0.
endmodule
