// Logisim project Exemplo0022_logisim.circ as structural Verilog: 4 circuits, main circuit main
module main (
  input  a3,
  input  a2,
  input  a1,
  input  a0,
  input  zero,
  input  b3,
  input  b2,
  input  b1,
  input  b0,
  output out_10,
  output out_11,
  output out_12,
  output out_13
);

  _4bitDiff u_4bitdiff_1 (
    .a3(a3), .a2(a2), .a1(a1), .a0(a0), .zero(zero), .b3(b3), .b2(b2), .b1(b1), .b0(b0), .s0(out_13),
    .s1(out_12), .s2(out_11), .s3(out_10));

  // Notes on the sheet:
  //   Não sei como usar uma constante, mas a entrada com rótulo "zero" deve ser sempre igual a 0.
endmodule

module halfDiff (
  input  a,
  input  b,
  output s0,
  output s1
);

  wire not_1_out;

  xor xor_1 (s0, a, b);
  not not_1 (not_1_out, a);
  and and_1 (s1, not_1_out, b);
endmodule

module fullDiff (
  input  a,
  input  b,
  input  c,
  output s0,
  output s1
);

  wire and_1_out, halfdiff_1_s0, halfdiff_1_s1, not_1_out;

  halfDiff halfdiff_1 (.a(a), .b(b), .s0(halfdiff_1_s0), .s1(halfdiff_1_s1));
  not not_1 (not_1_out, halfdiff_1_s0);
  and and_1 (and_1_out, not_1_out, c);
  xor xor_1 (s0, halfdiff_1_s0, c);
  or or_1 (s1, halfdiff_1_s1, and_1_out);
endmodule

module _4bitDiff (
  input  a3,
  input  a2,
  input  a1,
  input  a0,
  input  zero,
  input  b3,
  input  b2,
  input  b1,
  input  b0,
  output s0,
  output s1,
  output s2,
  output s3
);

  wire fulldiff_1_s1, fulldiff_2_s1, fulldiff_3_s1;

  fullDiff fulldiff_1 (.a(a0), .b(b0), .c(zero), .s0(s0), .s1(fulldiff_1_s1));
  fullDiff fulldiff_2 (.a(a1), .b(b1), .c(fulldiff_1_s1), .s0(s1), .s1(fulldiff_2_s1));
  fullDiff fulldiff_3 (.a(a2), .b(b2), .c(fulldiff_2_s1), .s0(s2), .s1(fulldiff_3_s1));
  fullDiff fulldiff_4 (.a(a3), .b(b3), .c(fulldiff_3_s1), .s0(s3));  // open: s1

  // Notes on the sheet:
  //   Não sei como usar uma constante, mas a entrada com rótulo "zero" deve ser sempre igual a 0.
endmodule
