// Logisim project Exemplo0023_logisim.circ as structural Verilog: 2 circuits, main circuit main
module main (
  input  a0,
  input  a1,
  input  a2,
  input  a3,
  input  b0,
  input  b1,
  input  b2,
  input  b3,
  output s
);

  subcircuito subcircuito_1 (.a0(a0), .a1(a1), .a2(a2), .a3(a3), .b0(b0), .b1(b1), .b2(b2), .b3(b3), .s(s));
endmodule

module subcircuito (
  input  a0,
  input  a1,
  input  a2,
  input  a3,
  input  b0,
  input  b1,
  input  b2,
  input  b3,
  output s
);

  wire xnor_1_out, xnor_2_out, xnor_3_out, xnor_4_out;

  xnor xnor_1 (xnor_1_out, a0, b0);
  xnor xnor_2 (xnor_2_out, a1, b1);
  xnor xnor_3 (xnor_3_out, a2, b2);
  xnor xnor_4 (xnor_4_out, a3, b3);
  and and_1 (s, xnor_1_out, xnor_2_out, xnor_3_out, xnor_4_out);
endmodule
