// Logisim project Exemplo0025_logisim.circ as structural Verilog: 2 circuits, main circuit main
module main (
  input  a3,
  input  a2,
  input  a1,
  input  a0,
  input  um,
  output s3,
  output s2,
  output s1,
  output s0
);

  C2 c2_1 (.a3(a3), .a2(a2), .a1(a1), .a0(a0), .um(um), .s0(s0), .s1(s1), .s2(s2), .s3(s3));

  // Notes on the sheet:
  //   Não sei como usar uma constante, mas a entrada com rótulo "um" deve ser sempre igual a 1.
endmodule

module C2 (
  input  a3,
  input  a2,
  input  a1,
  input  a0,
  input  um,
  output s0,
  output s1,
  output s2,
  output s3
);

  wire not_1_out, xor_1_out, xor_2_out, xor_3_out, xor_4_out;

  not not_1 (not_1_out, um);
  xor xor_1 (xor_1_out, a3, um);
  xor xor_2 (xor_2_out, a2, um);
  xor xor_3 (xor_3_out, a1, um);
  xor xor_4 (xor_4_out, a0, um);
  _4bitAdder u_4bitadder_1 (
    .a3(xor_1_out), .a2(xor_2_out), .a1(xor_3_out), .a0(xor_4_out), .zero(not_1_out), .b3(not_1_out),
    .b2(not_1_out), .b1(not_1_out), .b0(um), .s0(s0), .s1(s1), .s2(s2), .s3(s3));  // open: carry

  // Notes on the sheet:
  //   Não sei como usar uma constante, mas a entrada com rótulo "um" deve ser sempre igual a 1.
endmodule
