// Logisim project Ex0021.circ as structural Verilog: 3 circuits, main circuit adder
module adder (
  input  x,
  input  y,
  output s0,
  output s1
);

  xor XOR1 (s0, x, y);
  and AND1 (s1, y, x);
endmodule

// FA
module fulladder (
  input  c,
  input  x,
  input  y,
  output out_4,
  output out_5
);

  wire adder_1_s0, adder_1_s1, adder_2_s1;

  adder adder_1 (.x(x), .y(y), .s0(adder_1_s0), .s1(adder_1_s1));
  adder adder_2 (.x(adder_1_s0), .y(c), .s0(out_4), .s1(adder_2_s1));
  or OR1 (out_5, adder_2_s1, adder_1_s1);
endmodule

module main (
  input  Carry_in,
  input  X,
  input  X_2,
  input  X_3,
  input  sinal,
  input  Y,
  input  Y_2,
  input  Y_3,
  input  sinal_2,
  output out_10,
  output out_11,
  output out_12,
  output out_13,
  output Carry_out
);

  wire fulladder_1_out_5, fulladder_2_out_5, fulladder_3_out_5;

  fulladder fulladder_1 (.x(X), .y(Y), .c(Carry_in), .out_5(fulladder_1_out_5), .out_4(out_10));
  fulladder fulladder_2 (.x(Y_2), .y(X_2), .c(fulladder_1_out_5), .out_5(fulladder_2_out_5), .out_4(out_11));
  fulladder fulladder_3 (.x(X_3), .y(Y_3), .c(fulladder_2_out_5), .out_5(fulladder_3_out_5), .out_4(out_12));
  fulladder fulladder_4 (.x(sinal), .y(sinal_2), .c(fulladder_3_out_5), .out_5(Carry_out), .out_4(out_13));
endmodule
