// Logisim project Ex0022_CORRIGIDO.circ as structural Verilog: 3 circuits, main circuit MD
// md
module MD (
  input  x,
  input  y,
  output s0,
  output s1
);

  wire not_1_out;

  xor XOR1 (s0, x, y);
  not not_1 (not_1_out, x);
  and AND1 (s1, not_1_out, y);
endmodule

// fd
module FD (
  input  c,
  input  x,
  input  y,
  output s1,
  output s2
);

  wire md_1_s0, md_1_s1, md_2_s1;

  MD md_1 (.x(x), .y(y), .s0(md_1_s0), .s1(md_1_s1));
  MD md_2 (.x(md_1_s0), .y(c), .s0(s1), .s1(md_2_s1));
  or or_1 (s2, md_2_s1, md_1_s1);
endmodule

module main (
  input  Carry_in,
  input  X,
  input  X_2,
  input  X_3,
  input  Y,
  input  Y_2,
  input  Y_3,
  output out_8,
  output out_9,
  output out_10,
  output Carry_out
);

  wire fd_1_s2, fd_2_s2, XOR1_out, XOR2_out, XOR3_out;

  xor XOR1 (XOR1_out, Y, Carry_in);
  xor XOR2 (XOR2_out, X_2, Carry_in);
  xor XOR3 (XOR3_out, Y_3, Carry_in);
  FD fd_1 (.x(X), .y(XOR1_out), .c(Carry_in), .s2(fd_1_s2), .s1(out_8));
  FD fd_2 (.x(Y_2), .y(XOR2_out), .c(fd_1_s2), .s2(fd_2_s2), .s1(out_9));
  FD fd_3 (.x(X_3), .y(XOR3_out), .c(fd_2_s2), .s2(Carry_out), .s1(out_10));
endmodule
