// Logisim project Ex0024.circ as structural Verilog: 1 circuit, main circuit main
module main (
  input  in_1,
  input  in_2,
  input  in_3,
  input  in_4,
  input  in_5,
  input  in_6,
  input  in_7,
  input  in_8,
  output s
);

  wire [3:0] XNOR1_out;

  assign XNOR1_out = ~({in_1, in_2, in_3, in_4} ^ {in_5, in_6, in_7, in_8});  // XNOR_Gate XNOR1, 4 bits wide
  nand NAND1 (s, XNOR1_out[0], XNOR1_out[1], XNOR1_out[2], XNOR1_out[3]);

  // Notes on the sheet:
  //   0 = Igual
  //   1 = Diferente
endmodule
