// Logisim project Ex0025.circ as structural Verilog: 3 circuits, main circuit adder
module adder (
  input  x,
  input  y,
  output s0,
  output s1
);

  xor XOR1 (s0, x, y);
  and AND1 (s1, y, x);
endmodule

module fulladder (
  input  c,
  input  x,
  input  y,
  output out_4,
  output out_5
);

  wire adder_1_s0, adder_1_s1, adder_2_s1;

  adder adder_1 (.x(x), .y(y), .s0(adder_1_s0), .s1(adder_1_s1));
  adder adder_2 (.x(adder_1_s0), .y(c), .s0(out_4), .s1(adder_2_s1));
  or OR1 (out_5, adder_2_s1, adder_1_s1);
endmodule

module main (
  input  Carry_in,
  input  x,
  input  y,
  input  z,
  input  w,
  output out_6,
  output out_7,
  output out_8,
  output out_9,
  output Carry_out
);

  wire fulladder_1_out_5, fulladder_2_out_5, fulladder_3_out_5, NOT1_out, NOT2_out, NOT3_out, NOT4_out;

  not NOT1 (NOT1_out, x);
  not NOT2 (NOT2_out, y);
  not NOT3 (NOT3_out, z);
  not NOT4 (NOT4_out, w);
  fulladder fulladder_1 (.x(NOT1_out), .y(1'b1), .c(Carry_in), .out_5(fulladder_1_out_5), .out_4(out_6));
  fulladder fulladder_2 (.x(NOT2_out), .y(1'b0), .c(fulladder_1_out_5), .out_5(fulladder_2_out_5), .out_4(out_7));
  fulladder fulladder_3 (.x(NOT3_out), .y(1'b0), .c(fulladder_2_out_5), .out_5(fulladder_3_out_5), .out_4(out_8));
  fulladder fulladder_4 (.x(NOT4_out), .y(1'b0), .c(fulladder_3_out_5), .out_5(Carry_out), .out_4(out_9));
endmodule
