// Logisim project Exemplo0022.circ as structural Verilog: 3 circuits, main circuit main
module main (
  input  Carry_in,
  input  Amplitude,
  input  Sinal,
  input  in_4,
  input  in_5,
  input  in_6,
  input  in_7,
  input  in_8,
  input  in_9,
  output Sinal_2,
  output Carry_out,
  output Amplitude_2,
  output out_13,
  output out_14
);

  wire fulladder_1_carry_out, fulladder_2_carry_out, fulladder_3_carry_out;

  fullAdder fulladder_1 (.x(Amplitude), .y(in_6), .Carry_in(Carry_in), .Carry_out(fulladder_1_carry_out), .s2(out_14));
  fullAdder fulladder_2 (
    .x(in_5), .y(in_9), .Carry_in(fulladder_1_carry_out), .Carry_out(fulladder_2_carry_out), .s2(out_13));
  fullAdder fulladder_3 (
    .x(in_4), .y(in_8), .Carry_in(fulladder_2_carry_out), .Carry_out(fulladder_3_carry_out), .s2(Amplitude_2));
  fullAdder fulladder_4 (.x(Sinal), .y(in_7), .Carry_in(fulladder_3_carry_out), .Carry_out(Sinal_2), .s2(Carry_out));
endmodule

module Adder (
  input  a,
  input  b,
  output s0,
  output s1
);

  xor XOR1 (s0, a, b);
  and AND1 (s1, b, a);
endmodule

// F.Adder
module fullAdder (
  input  x,
  input  y,
  input  Carry_in,
  output s2,
  output Carry_out
);

  wire adder_1_s0, adder_1_s1, adder_2_s1;

  Adder adder_1 (.a(y), .b(x), .s0(adder_1_s0), .s1(adder_1_s1));
  Adder adder_2 (.a(adder_1_s0), .b(Carry_in), .s0(s2), .s1(adder_2_s1));
  or OR1 (Carry_out, adder_2_s1, adder_1_s1);
endmodule
