// Logisim project Exemplo0023.circ as structural Verilog: 2 circuits, main circuit main
module main (
  input  Amplitude,
  input  Sinal,
  input  in_3,
  input  in_4,
  input  in_5,
  input  in_6,
  input  in_7,
  input  in_8,
  output s
);

  wire comp_igual_1_s1, comp_igual_2_s1, comp_igual_3_s1, comp_igual_4_s1;

  Comp_Igual comp_igual_1 (.a(Amplitude), .b(in_5), .s1(comp_igual_1_s1));
  Comp_Igual comp_igual_2 (.a(in_4), .b(in_8), .s1(comp_igual_2_s1));
  Comp_Igual comp_igual_3 (.a(in_3), .b(in_7), .s1(comp_igual_3_s1));
  Comp_Igual comp_igual_4 (.a(Sinal), .b(in_6), .s1(comp_igual_4_s1));
  and and_1 (s, comp_igual_1_s1, comp_igual_2_s1, comp_igual_3_s1, comp_igual_4_s1);

  // Notes on the sheet:
  //   s = 1 -- Iguais
  //   s = 0 -- Diferentes
endmodule

// C.I.
module Comp_Igual (
  input  a,
  input  b,
  output s1
);

  wire AND1_out, AND2_out, NOT1_out, NOT2_out;

  not NOT1 (NOT1_out, a);
  not NOT2 (NOT2_out, b);
  and AND1 (AND1_out, NOT1_out, NOT2_out);
  and AND2 (AND2_out, a, b);
  or OR1 (s1, AND1_out, AND2_out);
endmodule
