// Logisim project Exemplo0024.circ as structural Verilog: 2 circuits, main circuit main
module main (
  input  Amplitude,
  input  Sinal,
  input  in_3,
  input  in_4,
  input  in_5,
  input  in_6,
  input  in_7,
  input  in_8,
  output s
);

  wire \comp_diferença_1_s1 , \comp_diferença_2_s1 , \comp_diferença_3_s1 , \comp_diferença_4_s1 ;

  \Comp_Diferença  \comp_diferença_1  (.a(Amplitude), .b(in_5), .s1(\comp_diferença_1_s1 ));
  \Comp_Diferença  \comp_diferença_2  (.a(in_4), .b(in_8), .s1(\comp_diferença_2_s1 ));
  \Comp_Diferença  \comp_diferença_3  (.a(in_3), .b(in_7), .s1(\comp_diferença_3_s1 ));
  \Comp_Diferença  \comp_diferença_4  (.a(Sinal), .b(in_6), .s1(\comp_diferença_4_s1 ));
  or OR2 (s, \comp_diferença_1_s1 , \comp_diferença_2_s1 , \comp_diferença_3_s1 , \comp_diferença_4_s1 );

  // Notes on the sheet:
  //   s = 0 -- Iguais
  //   s = 1 -- Diferentes
endmodule

// C.D.
module \Comp_Diferença  (
  input  a,
  input  b,
  output s1
);

  wire AND1_out, AND2_out, NOT1_out, NOT2_out;

  not NOT1 (NOT1_out, a);
  not NOT2 (NOT2_out, b);
  and AND1 (AND1_out, NOT1_out, b);
  and AND2 (AND2_out, a, NOT2_out);
  or OR1 (s1, AND1_out, AND2_out);
endmodule
