// Logisim project Exemplo0025.circ as structural Verilog: 3 circuits, main circuit main
module main (
  input  Sinal,
  input  Amplitude,
  input  in_3,
  input  in_4,
  output Sinal_2,
  output Amplitude_2,
  output out_7,
  output out_8,
  output out_9
);

  wire fulladder_1_carry_out, fulladder_2_carry_out, fulladder_3_carry_out, not_1_out, not_2_out, not_3_out,
       not_4_out;

  not not_1 (not_1_out, in_4);
  not not_2 (not_2_out, in_3);
  not not_3 (not_3_out, Amplitude);
  not not_4 (not_4_out, Sinal);
  fullAdder fulladder_1 (.x(1'b0), .y(not_1_out), .Carry_in(1'b1), .Carry_out(fulladder_1_carry_out), .s2(out_8));
  fullAdder fulladder_2 (
    .x(1'b0), .y(not_2_out), .Carry_in(fulladder_1_carry_out), .Carry_out(fulladder_2_carry_out), .s2(out_7));
  fullAdder fulladder_3 (
    .x(1'b0), .y(not_3_out), .Carry_in(fulladder_2_carry_out), .Carry_out(fulladder_3_carry_out),
    .s2(Amplitude_2));
  fullAdder fulladder_4 (.x(1'b0), .y(not_4_out), .Carry_in(fulladder_3_carry_out), .Carry_out(out_9), .s2(Sinal_2));
endmodule

module Adder (
  input  a,
  input  b,
  output s1,
  output s2
);

  and AND1 (s2, a, b);
  xor XOR1 (s1, a, b);
endmodule

module fullAdder (
  input  x,
  input  y,
  input  Carry_in,
  output s2,
  output Carry_out
);

  wire adder_1_s1, adder_1_s2, adder_2_s2;

  Adder adder_1 (.a(y), .b(x), .s1(adder_1_s1), .s2(adder_1_s2));
  Adder adder_2 (.a(adder_1_s1), .b(Carry_in), .s1(s2), .s2(adder_2_s2));
  or OR1 (Carry_out, adder_2_s2, adder_1_s2);
endmodule
