// Logisim project Exemplo0022.circ as structural Verilog: 3 circuits, main circuit main
module main (
  input  Sinal,
  input  Amplitude,
  input  Sinal_2,
  input  in_4,
  input  in_5,
  input  in_6,
  input  in_7,
  input  in_8,
  input  in_9,
  output out_10,
  output Carry_out,
  output Amplitude_2,
  output out_13,
  output out_14
);

  wire fulldif_1_out_5, fulldif_2_out_5, fulldif_3_out_5;

  fullDif fulldif_1 (.in_1(Amplitude), .in_2(in_6), .in_3(Sinal), .out_5(fulldif_1_out_5), .out_4(out_14));
  fullDif fulldif_2 (.in_1(in_5), .in_2(in_9), .in_3(fulldif_1_out_5), .out_5(fulldif_2_out_5), .out_4(out_13));
  fullDif fulldif_3 (.in_1(in_4), .in_2(in_8), .in_3(fulldif_2_out_5), .out_5(fulldif_3_out_5), .out_4(Amplitude_2));
  fullDif fulldif_4 (.in_1(Sinal_2), .in_2(in_7), .in_3(fulldif_3_out_5), .out_5(out_10), .out_4(Carry_out));

  // Notes on the sheet:
  //   Carry_in
endmodule

// F.D.
module fullDif (
  input  in_1,
  input  in_2,
  input  in_3,
  output out_4,
  output out_5
);

  wire dif_1_out_3, dif_1_out_4, dif_2_out_4;

  Dif dif_1 (.in_1(in_1), .in_2(in_2), .out_3(dif_1_out_3), .out_4(dif_1_out_4));
  Dif dif_2 (.in_1(dif_1_out_3), .in_2(in_3), .out_3(out_4), .out_4(dif_2_out_4));
  or OR1 (out_5, dif_2_out_4, dif_1_out_4);
endmodule

module Dif (
  input  in_1,
  input  in_2,
  output out_3,
  output out_4
);

  wire NOT1_out;

  not NOT1 (NOT1_out, in_1);
  and AND (out_4, NOT1_out, in_2);
  xor XOR1 (out_3, in_1, in_2);
endmodule
