// Logisim project Exemplo0027.circ as structural Verilog: 4 circuits, main circuit main
module main (
  input  a,
  input  b,
  input  Chave,
  output s
);

  wire dif_1_s1, igualdade_1_s1;

  Dif dif_1 (.a(a), .b(b), .s1(dif_1_s1));
  Igualdade igualdade_1 (.a(a), .b(b), .s1(igualdade_1_s1));
  Selecionador selecionador_1 (.a(dif_1_s1), .b(igualdade_1_s1), .Chave(Chave), .s1(s));

  // Notes on the sheet:
  //   0 -- Diferença
  //   1 -- Igualdade
endmodule

// DIF
module Dif (
  input  a,
  input  b,
  output s1
);

  wire AND1_out, AND2_out, NOT1_out, NOT2_out;

  not NOT1 (NOT1_out, a);
  not NOT2 (NOT2_out, b);
  and AND1 (AND1_out, NOT1_out, b);
  and AND2 (AND2_out, a, NOT2_out);
  or OR1 (s1, AND1_out, AND2_out);
endmodule

// Igua.
module Igualdade (
  input  a,
  input  b,
  output s1
);

  wire AND1_out, AND2_out, NOT1_out, NOT2_out;

  not NOT1 (NOT1_out, a);
  not NOT2 (NOT2_out, b);
  and AND1 (AND1_out, NOT1_out, NOT2_out);
  and AND2 (AND2_out, a, b);
  or OR1 (s1, AND1_out, AND2_out);
endmodule

// MUX
module Selecionador (
  input  a,
  input  b,
  input  Chave,
  output s1
);

  wire AND1_out, AND2_out, NOT1_out;

  not NOT1 (NOT1_out, Chave);
  and AND1 (AND1_out, a, NOT1_out);
  and AND2 (AND2_out, Chave, b);
  or OR1 (s1, AND1_out, AND2_out);
endmodule
