// Logisim project Exemplo0022.circ as structural Verilog: 4 circuits, main circuit main
module main (
  input  [3:0] in_1,
  input  [3:0] in_2,
  output [3:0] out_3
);

  fullSubtract4 fullsubtract4_1 (.in_1(in_1), .in_2(in_2), .out_3(out_3));
endmodule

// HS
module halfSubtract (
  input  in_1,
  input  in_2,
  output s1,
  output s0
);

  xor xor_1 (s1, in_2, in_1);
  and and_1 (s0, in_2, ~in_1);  // AND_Gate
endmodule

// FS
module fullSubtract (
  input  in_1,
  input  in_2,
  input  in_3,
  output s1,
  output s0
);

  wire and_1_out, and_2_out, xor_1_out;

  xor xor_1 (xor_1_out, in_2, in_3);
  and and_1 (and_1_out, in_3, ~in_2);  // AND_Gate
  xor xor_2 (s1, in_1, xor_1_out);
  and and_2 (and_2_out, in_1, ~xor_1_out);  // AND_Gate
  or or_1 (s0, and_2_out, and_1_out);
endmodule

// FS4
module fullSubtract4 (
  input  [3:0] in_1,
  input  [3:0] in_2,
  output [3:0] out_3
);

  wire fullsubtract_1_s0, fullsubtract_2_s0, fullsubtract_3_s0, fullsubtract_3_s1, halfsubtract_1_s0;

  halfSubtract halfsubtract_1 (.in_1(in_1[0]), .in_2(in_2[0]), .s0(halfsubtract_1_s0), .s1(out_3[0]));
  fullSubtract fullsubtract_1 (
    .in_2(in_1[1]), .in_3(in_2[1]), .in_1(halfsubtract_1_s0), .s0(fullsubtract_1_s0), .s1(out_3[1]));
  fullSubtract fullsubtract_2 (
    .in_2(in_1[2]), .in_3(in_2[2]), .in_1(fullsubtract_1_s0), .s0(fullsubtract_2_s0), .s1(out_3[2]));
  fullSubtract fullsubtract_3 (
    .in_2(in_1[3]), .in_3(in_2[3]), .in_1(fullsubtract_2_s0), .s0(fullsubtract_3_s0), .s1(fullsubtract_3_s1));
  xor xor_1 (out_3[3], fullsubtract_3_s1, fullsubtract_3_s0);
endmodule
