// Logisim project Exemplo0024.circ as structural Verilog: 2 circuits, main circuit main
module main (
  input  [3:0] in_1,
  input  [3:0] in_2,
  output [3:0] out_3
);

  comparadorDiferenca comparadordiferenca_1 (.in_1(in_1), .in_2(in_2), .out_3(out_3));
endmodule

// CD
module comparadorDiferenca (
  input  [3:0] in_1,
  input  [3:0] in_2,
  output [3:0] out_3
);

  xor xor_1 (out_3[0], in_1[0], in_2[0]);
  xor xor_2 (out_3[1], in_2[1], in_1[1]);
  xor xor_3 (out_3[2], in_1[2], in_2[2]);
  xor xor_4 (out_3[3], in_1[3], in_2[3]);
endmodule
