// Logisim project Exemplo0021.circ as structural Verilog: 3 circuits, main circuit Halfadder
// HA
module Halfadder (
  input  b,
  input  a,
  output out_3,
  output out_4
);

  xor xor_1 (out_3, b, a);
  and and_1 (out_4, b, a);
endmodule

// FU
module Fulladder (
  input  in_1,
  input  a,
  input  b,
  output out_4,
  output out_5
);

  wire halfadder_1_out_3, halfadder_1_out_4, halfadder_2_out_4;

  Halfadder halfadder_1 (.b(a), .a(b), .out_3(halfadder_1_out_3), .out_4(halfadder_1_out_4));
  Halfadder halfadder_2 (.b(halfadder_1_out_3), .a(in_1), .out_3(out_4), .out_4(halfadder_2_out_4));
  or or_1 (out_5, halfadder_1_out_4, halfadder_2_out_4);
endmodule

module Fulladder2 (
  input  Carry_in,
  input  a0,
  input  a1,
  input  a2,
  input  Sinal_a,
  input  b0,
  input  b1,
  input  b2,
  input  Sinal_b,
  output out_10,
  output out_11,
  output Amplitude,
  output out_13,
  output out_14
);

  wire fulladder_1_out_5, fulladder_2_out_5, fulladder_3_out_5;

  Fulladder fulladder_1 (.a(a0), .b(b0), .in_1(Carry_in), .out_5(fulladder_1_out_5), .out_4(out_14));
  Fulladder fulladder_2 (.a(a1), .b(b1), .in_1(fulladder_1_out_5), .out_5(fulladder_2_out_5), .out_4(out_13));
  Fulladder fulladder_3 (.a(a2), .b(b2), .in_1(fulladder_2_out_5), .out_5(fulladder_3_out_5), .out_4(Amplitude));
  Fulladder fulladder_4 (.a(Sinal_a), .b(Sinal_b), .in_1(fulladder_3_out_5), .out_5(out_10), .out_4(out_11));
endmodule
