// Logisim project Exemplo0022.circ as structural Verilog: 3 circuits, main circuit difference
// HD
module difference (
  input  a,
  input  b,
  output s0,
  output s1
);

  wire not_1_out;

  not not_1 (not_1_out, a);
  xor xor_1 (s0, a, b);
  and and_1 (s1, not_1_out, b);
endmodule

// FD
module Full_difference (
  input  c,
  input  a,
  input  b,
  output s0,
  output s1
);

  wire difference_1_s0, difference_1_s1, difference_2_s1;

  difference difference_1 (.a(a), .b(b), .s0(difference_1_s0), .s1(difference_1_s1));
  difference difference_2 (.a(difference_1_s0), .b(c), .s0(s0), .s1(difference_2_s1));
  or or_1 (s1, difference_1_s1, difference_2_s1);
endmodule

module Full_difference2 (
  input  in_1,
  input  in_2,
  input  in_3,
  input  in_4,
  input  in_5,
  input  in_6,
  input  in_7,
  input  in_8,
  input  in_9,
  output out_10,
  output out_11,
  output out_12,
  output out_13,
  output out_14
);

  wire full_difference_1_s1, full_difference_2_s1, full_difference_3_s1;

  Full_difference full_difference_1 (.a(in_2), .b(in_6), .c(in_1), .s1(full_difference_1_s1), .s0(out_14));
  Full_difference full_difference_2 (
    .a(in_3), .b(in_7), .c(full_difference_1_s1), .s1(full_difference_2_s1), .s0(out_13));
  Full_difference full_difference_3 (
    .a(in_4), .b(in_8), .c(full_difference_2_s1), .s1(full_difference_3_s1), .s0(out_12));
  Full_difference full_difference_4 (.a(in_5), .b(in_9), .c(full_difference_3_s1), .s1(out_11), .s0(out_10));
endmodule
