// Logisim project Exemplo0023.circ as structural Verilog: 2 circuits, main circuit Equal1
// EQ
module Equal1 (
  input  a,
  input  b,
  output s0
);

  wire xnor_1_out;

  xnor xnor_1 (xnor_1_out, a, b);
  buf and_1 (s0, xnor_1_out);  // AND_Gate

  // Notes on the sheet:
  //   0 - Diferente
  //   1 - Igual
endmodule

module Equal2 (
  input  in_1,
  input  in_2,
  input  in_3,
  input  in_4,
  input  in_5,
  input  in_6,
  input  B,
  input  in_8,
  output out_9
);

  wire equal1_1_s0, equal1_2_s0, equal1_3_s0, equal1_4_s0;

  Equal1 equal1_1 (.a(in_1), .b(in_5), .s0(equal1_1_s0));
  Equal1 equal1_2 (.a(in_2), .b(in_6), .s0(equal1_2_s0));
  Equal1 equal1_3 (.a(in_3), .b(B), .s0(equal1_3_s0));
  Equal1 equal1_4 (.a(in_4), .b(in_8), .s0(equal1_4_s0));
  and and_1 (out_9, equal1_1_s0, equal1_2_s0, equal1_3_s0, equal1_4_s0);

  // Notes on the sheet:
  //   A
  //   0 - Diferente
  //   1 - Igual
endmodule
