// Logisim project Exemplo0024.circ as structural Verilog: 2 circuits, main circuit Diferença
// D
module \Diferença  (
  input  a,
  input  b,
  output s0
);

  wire xnor_1_out;

  xnor xnor_1 (xnor_1_out, a, b);
  not nand_1 (s0, xnor_1_out);  // NAND_Gate

  // Notes on the sheet:
  //   1 - Diferente
  //   0 - Igual
endmodule

module \Diferença2  (
  input  in_1,
  input  in_2,
  input  in_3,
  input  in_4,
  input  in_5,
  input  in_6,
  input  B,
  input  in_8,
  output out_9
);

  wire \diferença_1_s0 , \diferença_2_s0 , \diferença_3_s0 , \diferença_4_s0 ;

  \Diferença  \diferença_1  (.a(in_1), .b(in_5), .s0(\diferença_1_s0 ));
  \Diferença  \diferença_2  (.a(in_2), .b(in_6), .s0(\diferença_2_s0 ));
  \Diferença  \diferença_3  (.a(in_3), .b(B), .s0(\diferença_3_s0 ));
  \Diferença  \diferença_4  (.a(in_4), .b(in_8), .s0(\diferença_4_s0 ));
  or or_1 (out_9, \diferença_1_s0 , \diferença_2_s0 , \diferença_3_s0 , \diferença_4_s0 );

  // Notes on the sheet:
  //   A
  //   1 - Diferente
  //   0 - Igual
endmodule
