// Logisim project Exemplo0025.circ as structural Verilog: 3 circuits, main circuit Halfadder
// HA
module Halfadder (
  input  a,
  input  b,
  output s0,
  output s1
);

  xor XOR (s0, a, b);
  and AND (s1, b, a);
endmodule

// FU
module Fulladder (
  input  in_1,
  input  in_2,
  input  in_3,
  output out_4,
  output out_5
);

  wire halfadder_1_s0, halfadder_1_s1, halfadder_2_s1;

  Halfadder halfadder_1 (.a(in_2), .b(in_3), .s0(halfadder_1_s0), .s1(halfadder_1_s1));
  Halfadder halfadder_2 (.a(halfadder_1_s0), .b(in_1), .s0(out_4), .s1(halfadder_2_s1));
  or or_1 (out_5, halfadder_1_s1, halfadder_2_s1);
endmodule

module Complement (
  input  Carry_In,
  input  a,
  input  b,
  input  c,
  input  d,
  output out_6,
  output out_7,
  output out_8,
  output out_9,
  output Carry_Out
);

  wire fulladder_1_out_5, fulladder_2_out_5, fulladder_3_out_5, not_1_out, not_2_out, not_3_out, not_4_out;

  not not_1 (not_1_out, a);
  not not_2 (not_2_out, b);
  not not_3 (not_3_out, c);
  not not_4 (not_4_out, d);
  Fulladder fulladder_1 (.in_2(not_1_out), .in_3(1'b1), .in_1(Carry_In), .out_5(fulladder_1_out_5), .out_4(out_9));
  Fulladder fulladder_2 (
    .in_2(not_2_out), .in_3(1'b0), .in_1(fulladder_1_out_5), .out_5(fulladder_2_out_5), .out_4(out_8));
  Fulladder fulladder_3 (
    .in_2(not_3_out), .in_3(1'b0), .in_1(fulladder_2_out_5), .out_5(fulladder_3_out_5), .out_4(out_7));
  Fulladder fulladder_4 (.in_2(not_4_out), .in_3(1'b0), .in_1(fulladder_3_out_5), .out_5(Carry_Out), .out_4(out_6));
endmodule
