// Logisim project Guia4.circ as structural Verilog: 7 circuits, main circuit Soma Completa
// FA
module Soma_Completa (
  input  A,
  input  B,
  input  Carry_In,
  output S0,
  output Carry_Out
);

  wire and_1_out, and_2_out, xor_1_out, xor_2_out;

  xor xor_1 (xor_1_out, A, B);
  and and_1 (and_1_out, A, B);
  xor xor_2 (xor_2_out, A, B);
  and and_2 (and_2_out, Carry_In, xor_1_out);
  xor xor_3 (S0, xor_2_out, Carry_In);
  or or_1 (Carry_Out, and_2_out, and_1_out);
endmodule

module Diferenca_Completa (
  input  A,
  input  B,
  input  Carry_In,
  output S0,
  output Carry_Out
);

  wire and_1_out, and_2_out, not_1_out, not_2_out, or_1_out;

  xor xor_1 (S0, A, B);
  not not_1 (not_1_out, A);
  or or_1 (or_1_out, not_1_out, B);
  and and_1 (and_1_out, or_1_out, Carry_In);
  not not_2 (not_2_out, A);
  and and_2 (and_2_out, not_2_out, B);
  or or_2 (Carry_Out, and_1_out, and_2_out);
endmodule

// FA 4 bits
module Exercicio_1 (
  input  A,
  input  B,
  input  C,
  input  D,
  input  Carry_In,
  input  X,
  input  Y,
  input  Z,
  input  W,
  output snl,
  output s3,
  output s2,
  output s1,
  output s0
);

  wire soma_completa_1_carry_out, soma_completa_2_carry_out, soma_completa_3_carry_out;

  Soma_Completa soma_completa_1 (.A(D), .B(W), .Carry_In(Carry_In), .S0(s0), .Carry_Out(soma_completa_1_carry_out));
  Soma_Completa soma_completa_2 (
    .A(C), .B(Z), .Carry_In(soma_completa_1_carry_out), .S0(s1), .Carry_Out(soma_completa_2_carry_out));
  Soma_Completa soma_completa_3 (
    .A(B), .B(Y), .Carry_In(soma_completa_2_carry_out), .S0(s2), .Carry_Out(soma_completa_3_carry_out));
  Soma_Completa soma_completa_4 (.A(A), .B(X), .Carry_In(soma_completa_3_carry_out), .S0(s3), .Carry_Out(snl));
endmodule

// SUB 4 Bits
module Exercicio_2 (
  input  A,
  input  B,
  input  C,
  input  D,
  input  X,
  input  Y,
  input  Z,
  input  W,
  input  Carry_In,
  output snl,
  output s3,
  output s2,
  output s1,
  output s0
);

  wire diferenca_completa_1_carry_out, diferenca_completa_2_carry_out, diferenca_completa_3_carry_out;

  Diferenca_Completa diferenca_completa_1 (
    .A(D), .B(W), .Carry_In(Carry_In), .S0(s0), .Carry_Out(diferenca_completa_1_carry_out));
  Diferenca_Completa diferenca_completa_2 (
    .A(C), .B(Z), .Carry_In(diferenca_completa_1_carry_out), .S0(s1),
    .Carry_Out(diferenca_completa_2_carry_out));
  Diferenca_Completa diferenca_completa_3 (
    .A(B), .B(Y), .Carry_In(diferenca_completa_2_carry_out), .S0(s2),
    .Carry_Out(diferenca_completa_3_carry_out));
  Diferenca_Completa diferenca_completa_4 (
    .A(A), .B(X), .Carry_In(diferenca_completa_3_carry_out), .S0(s3), .Carry_Out(snl));
endmodule

module Exercicio_3 (
  input  [3:0] A,
  input  [3:0] B
);

  wire and_1_out, not_1_out, not_2_out, not_3_out, not_4_out, xor_1_out, xor_2_out, xor_3_out, xor_4_out;

  not not_1 (not_1_out, xor_1_out);
  xor xor_1 (xor_1_out, A[3], B[3]);
  xor xor_2 (xor_2_out, A[2], B[2]);
  not not_2 (not_2_out, xor_2_out);
  xor xor_3 (xor_3_out, A[1], B[1]);
  not not_3 (not_3_out, xor_3_out);
  xor xor_4 (xor_4_out, A[0], B[0]);
  not not_4 (not_4_out, xor_4_out);
  and and_1 (and_1_out, not_1_out, not_2_out, not_3_out, not_4_out);
  // Probe on and_1_out
endmodule

module Exercicio_4 (
  input  [3:0] A,
  input  [3:0] B
);

  wire or_1_out, xor_1_out, xor_2_out, xor_3_out, xor_4_out;

  xor xor_1 (xor_1_out, A[3], B[3]);
  xor xor_2 (xor_2_out, A[2], B[2]);
  xor xor_3 (xor_3_out, A[1], B[1]);
  xor xor_4 (xor_4_out, A[0], B[0]);
  or or_1 (or_1_out, xor_1_out, xor_2_out, xor_3_out, xor_4_out);
  // Probe on or_1_out
endmodule

// C2 4bits
module Exercicio_5 (
  input  X,
  input  Y,
  input  Z,
  input  W,
  output out_5,
  output out_6,
  output out_7,
  output out_8,
  output out_9
);

  wire exercicio_2_1_s0, exercicio_2_1_s1, exercicio_2_1_s2, exercicio_2_1_s3, exercicio_2_1_snl;

  Exercicio_2 exercicio_2_1 (
    .Carry_In(1'b0), .A(1'b1), .X(X), .B(1'b1), .Y(Y), .C(1'b1), .Z(Z), .D(1'b1), .W(W),
    .snl(exercicio_2_1_snl), .s3(exercicio_2_1_s3), .s2(exercicio_2_1_s2), .s1(exercicio_2_1_s1),
    .s0(exercicio_2_1_s0));
  Exercicio_1 exercicio_1_1 (
    .A(exercicio_2_1_s3), .B(exercicio_2_1_s2), .C(exercicio_2_1_s1), .D(exercicio_2_1_s0), .X(1'b0),
    .Y(1'b0), .Z(1'b0), .W(1'b1), .Carry_In(exercicio_2_1_snl), .snl(out_5), .s3(out_6), .s2(out_7),
    .s1(out_8), .s0(out_9));
endmodule
