// Logisim project Guia04.circ as structural Verilog: 15 circuits, main circuit main
module main (
  input  in_1,
  input  in_2,
  input  in_3,
  input  in_4,
  input  in_5,
  input  in_6,
  input  in_7,
  input  in_8,
  input  in_9,
  input  in_10,
  input  in_11,
  input  in_12,
  output out_13,
  output out_14,
  output out_15,
  output out_16,
  output out_17,
  output out_18
);

  wire full_adder_2_s1, full_adder_3_s1, full_adder_4_s1, full_adder_5_s1, half_adder_1_s1;

  Full_Adder full_adder_1 (.carry_in(full_adder_2_s1), .s0(out_13), .a(in_1), .b(in_7));  // open: s1
  Full_Adder full_adder_2 (.carry_in(full_adder_3_s1), .s1(full_adder_2_s1), .s0(out_14), .a(in_2), .b(in_8));
  Full_Adder full_adder_3 (.carry_in(full_adder_4_s1), .s1(full_adder_3_s1), .s0(out_15), .a(in_3), .b(in_9));
  Full_Adder full_adder_4 (.carry_in(full_adder_5_s1), .s1(full_adder_4_s1), .s0(out_16), .a(in_4), .b(in_10));
  Full_Adder full_adder_5 (.carry_in(half_adder_1_s1), .s1(full_adder_5_s1), .s0(out_17), .a(in_5), .b(in_11));
  Half_Adder half_adder_1 (.s1(half_adder_1_s1), .s0(out_18), .a(in_6), .b(in_12));
endmodule

module Exemplo0021 (
  input  in_1,
  input  in_2,
  input  in_3,
  input  in_4,
  input  in_5,
  input  in_6,
  input  in_7,
  input  in_8,
  input  in_9,
  input  in_10,
  input  in_11,
  input  in_12,
  output out_13,
  output out_14,
  output out_15,
  output out_16,
  output out_17,
  output out_18
);

  wire full_adder_1_s1, full_adder_2_s1, full_adder_3_s1, full_adder_4_s1, half_adder_1_s1, xor_1_out;

  xor xor_1 (xor_1_out, in_7, full_adder_1_s1);
  xor xor_2 (out_13, in_1, xor_1_out);
  Full_Adder full_adder_1 (.carry_in(full_adder_2_s1), .s1(full_adder_1_s1), .s0(out_14), .a(in_2), .b(in_8));
  Full_Adder full_adder_2 (.carry_in(full_adder_3_s1), .s1(full_adder_2_s1), .s0(out_15), .a(in_3), .b(in_9));
  Full_Adder full_adder_3 (.carry_in(full_adder_4_s1), .s1(full_adder_3_s1), .s0(out_16), .a(in_4), .b(in_10));
  Full_Adder full_adder_4 (.carry_in(half_adder_1_s1), .s1(full_adder_4_s1), .s0(out_17), .a(in_5), .b(in_11));
  Half_Adder half_adder_1 (.s1(half_adder_1_s1), .s0(out_18), .a(in_6), .b(in_12));
endmodule

module Exemplo0022 (
  input  in_1,
  input  in_2,
  input  in_3,
  input  in_4,
  input  in_5,
  input  in_6,
  input  in_7,
  input  in_8,
  input  in_9,
  input  in_10,
  input  in_11,
  input  in_12,
  output out_13,
  output out_14,
  output out_15,
  output out_16,
  output out_17,
  output out_18
);

  wire full_subtractor_1_s1, full_subtractor_2_s1, full_subtractor_3_s1, full_subtractor_4_s1,
       half_subtractor_1_s1, xor_1_out;

  xor xor_1 (xor_1_out, in_7, full_subtractor_1_s1);
  xor xor_2 (out_13, in_1, xor_1_out);
  Full_Subtractor full_subtractor_1 (
    .borrow_in(full_subtractor_2_s1), .s1(full_subtractor_1_s1), .s0(out_14), .a(in_2), .b(in_8));
  Full_Subtractor full_subtractor_2 (
    .borrow_in(full_subtractor_3_s1), .s1(full_subtractor_2_s1), .s0(out_15), .a(in_3), .b(in_9));
  Full_Subtractor full_subtractor_3 (
    .borrow_in(full_subtractor_4_s1), .s1(full_subtractor_3_s1), .s0(out_16), .a(in_4), .b(in_10));
  Full_Subtractor full_subtractor_4 (
    .borrow_in(half_subtractor_1_s1), .s1(full_subtractor_4_s1), .s0(out_17), .a(in_5), .b(in_11));
  Half_Subtractor half_subtractor_1 (.s1(half_subtractor_1_s1), .s0(out_18), .a(in_6), .b(in_12));
endmodule

// EQ
module Exemplo0023 (
  input  in_1,
  input  in_2,
  input  in_3,
  input  in_4,
  input  in_5,
  input  in_6,
  input  in_7,
  input  in_8,
  input  in_9,
  input  in_10,
  input  in_11,
  input  in_12,
  output out_13
);

  wire equals_1_s, equals_2_s, equals_3_s, equals_4_s, equals_5_s, equals_6_s;

  Equals equals_1 (.a(in_1), .b(in_7), .s(equals_1_s));
  Equals equals_2 (.a(in_3), .b(in_9), .s(equals_2_s));
  Equals equals_3 (.a(in_2), .b(in_8), .s(equals_3_s));
  Equals equals_4 (.a(in_4), .b(in_10), .s(equals_4_s));
  and and_1 (out_13, equals_1_s, equals_3_s, equals_2_s, equals_4_s, equals_5_s, equals_6_s);
  Equals equals_5 (.a(in_5), .b(in_11), .s(equals_5_s));
  Equals equals_6 (.a(in_6), .b(in_12), .s(equals_6_s));
endmodule

// DF
module Exemplo0024 (
  input  in_1,
  input  in_2,
  input  in_3,
  input  in_4,
  input  in_5,
  input  in_6,
  input  in_7,
  input  in_8,
  input  in_9,
  input  in_10,
  input  in_11,
  input  in_12,
  output out_13
);

  wire different_1_s, different_2_s, different_3_s, different_4_s, different_5_s, different_6_s;

  Different different_1 (.a(in_1), .b(in_7), .s(different_1_s));
  Different different_2 (.a(in_2), .b(in_8), .s(different_2_s));
  Different different_3 (.a(in_3), .b(in_9), .s(different_3_s));
  Different different_4 (.a(in_4), .b(in_10), .s(different_4_s));
  or or_1 (out_13, different_1_s, different_2_s, different_3_s, different_4_s, different_5_s, different_6_s);
  Different different_5 (.a(in_5), .b(in_11), .s(different_5_s));
  Different different_6 (.a(in_6), .b(in_12), .s(different_6_s));
endmodule

module Exemplo0025 (
  input  in_1,
  input  in_2,
  input  in_3,
  input  in_4,
  input  in_5,
  input  in_6,
  output out_7,
  output out_8,
  output out_9,
  output out_10,
  output out_11,
  output out_12
);

  wire complement_1_1_out_7, complement_1_1_out_8, complement_1_1_out_9, complement_1_1_out_10,
       complement_1_1_out_11, complement_1_1_out_12, half_adder_1_s1, half_adder_2_s1, half_adder_3_s1,
       half_adder_4_s1, half_adder_5_s1, not_1_out, xor_2_out;

  xor xor_1 (out_7, complement_1_1_out_7, half_adder_1_s1);
  Half_Adder half_adder_1 (.s1(half_adder_1_s1), .s0(out_8), .a(complement_1_1_out_8), .b(half_adder_3_s1));
  Half_Adder half_adder_2 (.s1(half_adder_2_s1), .s0(out_10), .a(complement_1_1_out_10), .b(half_adder_4_s1));
  Half_Adder half_adder_3 (.s1(half_adder_3_s1), .s0(out_9), .a(complement_1_1_out_9), .b(half_adder_2_s1));
  Complement_1 complement_1_1 (
    .in_1(in_1), .in_2(in_2), .in_3(in_3), .in_4(in_4), .in_5(in_5), .in_6(in_6),
    .out_7(complement_1_1_out_7), .out_8(complement_1_1_out_8), .out_9(complement_1_1_out_9),
    .out_10(complement_1_1_out_10), .out_11(complement_1_1_out_11), .out_12(complement_1_1_out_12));
  Half_Adder half_adder_4 (.s1(half_adder_4_s1), .s0(out_11), .a(complement_1_1_out_11), .b(half_adder_5_s1));
  not not_1 (not_1_out, in_6);
  xor xor_2 (xor_2_out, in_6, not_1_out);
  Half_Adder half_adder_5 (.s1(half_adder_5_s1), .s0(out_12), .a(complement_1_1_out_12), .b(xor_2_out));
endmodule

// FA
module Full_Adder (
  input  carry_in,
  input  a,
  input  b,
  output s1,
  output s0
);

  wire and_1_out, and_2_out, xor_1_out;

  and and_1 (and_1_out, a, b);
  or or_1 (s1, and_1_out, and_2_out);
  and and_2 (and_2_out, carry_in, xor_1_out);
  xor xor_1 (xor_1_out, a, b);
  xor xor_2 (s0, carry_in, xor_1_out);
endmodule

// HA
module Half_Adder (
  input  a,
  input  b,
  output s1,
  output s0
);

  and and_1 (s1, a, b);
  xor xor_1 (s0, a, b);
endmodule

// HS
module Half_Subtractor (
  input  a,
  input  b,
  output s1,
  output s0
);

  wire not_1_out;

  not not_1 (not_1_out, a);
  and and_1 (s1, not_1_out, b);
  xor xor_1 (s0, a, b);
endmodule

// FS
module Full_Subtractor (
  input  borrow_in,
  input  a,
  input  b,
  output s1,
  output s0
);

  wire and_1_out, and_2_out, not_1_out, not_2_out, xor_1_out;

  not not_1 (not_1_out, a);
  and and_1 (and_1_out, not_1_out, b);
  or or_1 (s1, and_1_out, and_2_out);
  not not_2 (not_2_out, xor_1_out);
  and and_2 (and_2_out, borrow_in, not_2_out);
  xor xor_1 (xor_1_out, a, b);
  xor xor_2 (s0, borrow_in, xor_1_out);
endmodule

// E
module Equals (
  input  a,
  input  b,
  output s
);

  xnor xnor_1 (s, a, b);
endmodule

// D
module Different (
  input  a,
  input  b,
  output s
);

  xor xor_1 (s, a, b);
endmodule

// C1
module Complement_1 (
  input  in_1,
  input  in_2,
  input  in_3,
  input  in_4,
  input  in_5,
  input  in_6,
  output out_7,
  output out_8,
  output out_9,
  output out_10,
  output out_11,
  output out_12
);

  not not_1 (out_8, in_2);
  not not_2 (out_10, in_4);
  not not_3 (out_9, in_3);
  not not_4 (out_7, in_1);
  not not_5 (out_11, in_5);
  not not_6 (out_12, in_6);
endmodule

// AA
module Algebric_Adder (
  input  key,
  input  a,
  input  b,
  output s1,
  output s0
);

  wire and_1_out, and_2_out, or_1_out, xor_3_out, xor_4_out;

  and and_1 (and_1_out, a, xor_3_out);
  and and_2 (and_2_out, key, xor_4_out);
  or or_1 (or_1_out, and_1_out, and_2_out);
  xor xor_1 (s1, key, or_1_out);
  xor xor_2 (s0, key, xor_4_out);
  xor xor_3 (xor_3_out, key, b);
  xor xor_4 (xor_4_out, a, xor_3_out);
endmodule

module Exemplo0027 (
  input  in_1,
  input  in_2,
  input  in_3,
  input  in_4,
  input  in_5,
  input  in_6,
  input  in_7,
  input  in_8,
  input  in_9,
  input  in_10,
  input  in_11,
  input  in_12,
  input  key,
  output out_14
);

  wire exemplo0023_1_out_13;

  Exemplo0023 exemplo0023_1 (
    .in_1(in_1), .in_2(in_2), .in_3(in_3), .in_4(in_4), .in_5(in_5), .in_6(in_6), .in_7(in_7), .in_8(in_8),
    .in_9(in_9), .in_10(in_10), .in_11(in_11), .in_12(in_12), .out_13(exemplo0023_1_out_13));
  xor xor_1 (out_14, exemplo0023_1_out_13, key);

  // Notes on the sheet:
  //   0 = Equals
  //   1 = Different
endmodule
