// Logisim project Exemplo0021.circ as structural Verilog: 4 circuits, main circuit Exemplo0021
module Exemplo0021 (
  input  carry_in,
  input  [3:0] a,
  input  [3:0] b,
  output [3:0] s,
  output carry_out
);

  fullAdder2 fulladder2_1 (.a(a), .b(b), .Carry_in(carry_in), .Carry_out(carry_out), .S(s));

  // Notes on the sheet:
  //   Exemplo0021
endmodule

// HA
module halfAdder (
  input  a,
  input  b,
  output s,
  output Carry_out
);

  xor XOR (s, a, b);
  and AND (Carry_out, a, b);

  // Notes on the sheet:
  //   HalfAdder
endmodule

// FA
module fullAdder (
  input  Carry_in,
  input  a,
  input  b,
  output S,
  output Carry_out
);

  wire halfadder_1_carry_out, halfadder_1_s, halfadder_2_carry_out;

  halfAdder halfadder_1 (.a(a), .b(b), .s(halfadder_1_s), .Carry_out(halfadder_1_carry_out));
  halfAdder halfadder_2 (.a(halfadder_1_s), .b(Carry_in), .s(S), .Carry_out(halfadder_2_carry_out));
  or or_1 (Carry_out, halfadder_1_carry_out, halfadder_2_carry_out);

  // Notes on the sheet:
  //   FullAdder
endmodule

// FA2
module fullAdder2 (
  input  [3:0] a,
  input  [3:0] b,
  input  Carry_in,
  output [3:0] S,
  output Carry_out
);

  wire fulladder_1_carry_out, fulladder_2_carry_out, fulladder_3_carry_out;

  fullAdder fulladder_1 (.a(a[0]), .b(b[0]), .Carry_in(Carry_in), .Carry_out(fulladder_1_carry_out), .S(S[0]));
  fullAdder fulladder_2 (
    .a(a[1]), .b(b[1]), .Carry_in(fulladder_1_carry_out), .Carry_out(fulladder_2_carry_out), .S(S[1]));
  fullAdder fulladder_3 (
    .a(a[2]), .b(b[2]), .Carry_in(fulladder_2_carry_out), .Carry_out(fulladder_3_carry_out), .S(S[2]));
  fullAdder fulladder_4 (.a(a[3]), .b(b[3]), .Carry_in(fulladder_3_carry_out), .Carry_out(Carry_out), .S(S[3]));

  // Notes on the sheet:
  //   FullAdder 2
endmodule
