// Logisim project Exemplo0022.circ as structural Verilog: 4 circuits, main circuit Exemplo0022
module Exemplo0022 (
  input  Carry_in,
  input  [3:0] a,
  input  [3:0] b,
  output [3:0] S,
  output Carry_out
);

  Diferenca_Completa_2 diferenca_completa_2_1 (.a(a), .b(b), .Carry_in(Carry_in), .Carry_out(Carry_out), .S(S));

  // Notes on the sheet:
  //   Exemplo0022
endmodule

// MD
module Meia_Diferenca (
  input  a,
  input  b,
  output s,
  output Carry_out
);

  wire NOT_out;

  not NOT (NOT_out, a);
  xor XOR (s, a, b);
  and AND (Carry_out, NOT_out, b);
endmodule

// DC
module Diferenca_Completa (
  input  Carry_in,
  input  a,
  input  b,
  output S,
  output Carry_out
);

  wire meia_diferenca_1_carry_out, meia_diferenca_1_s, meia_diferenca_2_carry_out;

  Meia_Diferenca meia_diferenca_1 (.a(a), .b(b), .s(meia_diferenca_1_s), .Carry_out(meia_diferenca_1_carry_out));
  Meia_Diferenca meia_diferenca_2 (.a(meia_diferenca_1_s), .b(Carry_in), .s(S), .Carry_out(meia_diferenca_2_carry_out));
  or OR (Carry_out, meia_diferenca_1_carry_out, meia_diferenca_2_carry_out);
endmodule

// DC2
module Diferenca_Completa_2 (
  input  [3:0] a,
  input  [3:0] b,
  input  Carry_in,
  output [3:0] S,
  output Carry_out
);

  wire diferenca_completa_1_carry_out, diferenca_completa_2_carry_out, diferenca_completa_3_carry_out;

  Diferenca_Completa diferenca_completa_1 (
    .a(a[0]), .b(b[0]), .Carry_in(Carry_in), .Carry_out(diferenca_completa_1_carry_out), .S(S[0]));
  Diferenca_Completa diferenca_completa_2 (
    .a(a[1]), .b(b[1]), .Carry_in(diferenca_completa_1_carry_out),
    .Carry_out(diferenca_completa_2_carry_out), .S(S[1]));
  Diferenca_Completa diferenca_completa_3 (
    .a(a[2]), .b(b[2]), .Carry_in(diferenca_completa_2_carry_out),
    .Carry_out(diferenca_completa_3_carry_out), .S(S[2]));
  Diferenca_Completa diferenca_completa_4 (
    .a(a[3]), .b(b[3]), .Carry_in(diferenca_completa_3_carry_out), .Carry_out(Carry_out), .S(S[3]));
endmodule
