// Logisim project Exemplo0023.circ as structural Verilog: 3 circuits, main circuit Exemplo0023
module Exemplo0023 (
  input  [3:0] a,
  input  [3:0] b,
  output S
);

  Igualdade2 igualdade2_1 (.a(a), .b(b), .S(S));

  // Notes on the sheet:
  //   Exemplo0023
endmodule

// ==
module Igualdade (
  input  a,
  input  b,
  output s
);

  xnor XNOR (s, a, b);

  // Notes on the sheet:
  //   Igualdade
endmodule

// ==2
module Igualdade2 (
  input  [3:0] a,
  input  [3:0] b,
  output S
);

  wire igualdade_1_s, igualdade_2_s, igualdade_3_s, igualdade_4_s;

  Igualdade igualdade_1 (.a(a[0]), .b(b[0]), .s(igualdade_1_s));
  Igualdade igualdade_2 (.a(a[1]), .b(b[1]), .s(igualdade_2_s));
  Igualdade igualdade_3 (.a(a[2]), .b(b[2]), .s(igualdade_3_s));
  Igualdade igualdade_4 (.a(a[3]), .b(b[3]), .s(igualdade_4_s));
  and AND (S, igualdade_1_s, igualdade_2_s, igualdade_3_s, igualdade_4_s);

  // Notes on the sheet:
  //   Igualdade 2
endmodule
