// Logisim project Exemplo0021.circ as structural Verilog: 3 circuits, main circuit main
module main (
  input  [3:0] bits_a,
  input  [3:0] bits_b,
  input  Carry_in,
  output [3:0] Saida,
  output Carry_out
);

  wire A_carry_out, B_carry_out, C_carry_out;

  FullAdder A (.a(bits_b[0]), .b(bits_a[0]), .Carry_in(Carry_in), .Carry_out(A_carry_out), .s(Saida[0]));
  FullAdder B (.a(bits_b[1]), .b(bits_a[1]), .Carry_in(A_carry_out), .Carry_out(B_carry_out), .s(Saida[1]));
  FullAdder C (.a(bits_b[2]), .b(bits_a[2]), .Carry_in(B_carry_out), .Carry_out(C_carry_out), .s(Saida[2]));
  FullAdder D (.a(bits_a[3]), .b(bits_b[3]), .Carry_in(C_carry_out), .Carry_out(Carry_out), .s(Saida[3]));

  // Notes on the sheet:
  //   Full Adder para 4 Bits
  //   b0
  //   a0
  //   c0
  //   b1
  //   a1
  //   c1
  //   b2
  //   a2
  //   c2
  //   b3
  //   a3
  //   c3
endmodule

// H.A.
module halfAdder (
  input  Carry_in,
  input  a,
  output s,
  output Carry_out
);

  xor xor_1 (Carry_out, Carry_in, a);
  and and_1 (s, a, Carry_in);

  // Notes on the sheet:
  //   Carry in
  //   a
  //   a
  //   Carry in
endmodule

// F.A.
module FullAdder (
  input  Carry_in,
  input  a,
  input  b,
  output s,
  output Carry_out
);

  wire A_carry_out, A_s, B_s;

  halfAdder u_A (.a(a), .Carry_in(Carry_in), .Carry_out(A_carry_out), .s(A_s));
  halfAdder u_B (.a(b), .Carry_in(A_carry_out), .Carry_out(s), .s(B_s));
  or C (Carry_out, A_s, B_s);

  // Notes on the sheet:
  //   c0
  //   s
  //   s0
  //   s1
endmodule
