// Logisim project Exemplo0022.circ as structural Verilog: 4 circuits, main circuit main
module main (
  input  [3:0] a,
  input  [3:0] b,
  input  Carrry_In,
  output [3:0] Saida,
  output Carry_Out
);

  wire A_carry_out, B_carry_out, C_carry_out;

  FullSubtractorCompact u_A (.a(a[0]), .b(b[0]), .Carry_in(Carrry_In), .Carry_Out(A_carry_out), .s0(Saida[0]));
  FullSubtractorCompact u_B (.a(a[1]), .b(b[1]), .Carry_in(A_carry_out), .Carry_Out(B_carry_out), .s0(Saida[1]));
  FullSubtractorCompact C (.a(a[2]), .b(b[2]), .Carry_in(B_carry_out), .Carry_Out(C_carry_out), .s0(Saida[2]));
  FullSubtractorCompact D (.a(a[3]), .b(b[3]), .Carry_in(C_carry_out), .Carry_Out(Carry_Out), .s0(Saida[3]));

  // Notes on the sheet:
  //   Subtrator Completo para 4 Bits
  //   s0
  //   x1
  //   s1
  //   x2
  //   s2
  //   x3
  //   s3
endmodule

module FullSubtractor (
  input  Carry_in,
  input  a,
  input  b,
  output Carry_Out,
  output s0
);

  wire A_out, B_out, D_out, N1_out, N2_out;

  not N1 (N1_out, a);
  xor u_A (A_out, a, b);
  and u_B (B_out, N1_out, b);
  not N2 (N2_out, A_out);
  xor C (s0, A_out, Carry_in);
  and D (D_out, N2_out, Carry_in);
  or E (Carry_Out, D_out, B_out);
endmodule

// H.S.
module halfSubtractor (
  input  Carry_In,
  input  a,
  output s0,
  output Carry_Out
);

  wire N1_out;

  xor u_A (s0, a, Carry_In);
  not N1 (N1_out, a);
  and B (Carry_Out, N1_out, Carry_In);
endmodule

// F.S.
module FullSubtractorCompact (
  input  Carry_in,
  input  a,
  input  b,
  output s0,
  output Carry_Out
);

  wire A_carry_out, A_s0, B_carry_out;

  halfSubtractor u_A (.a(a), .Carry_In(b), .Carry_Out(A_carry_out), .s0(A_s0));
  halfSubtractor u_B (.a(A_s0), .Carry_In(Carry_in), .Carry_Out(B_carry_out), .s0(s0));
  or C (Carry_Out, B_carry_out, A_carry_out);

  // Notes on the sheet:
  //   x1
  //   x2
  //   x1
  //   x3
  //   x3
  //   x2
endmodule
