// Logisim project Exemplo0023.circ as structural Verilog
module main (
  input  [3:0] a,
  input  [3:0] b,
  output Saida
);

  wire A_saida, B_saida;

  Comparador2BitsIguais u_A (.a0(b[0]), .a2(a[0]), .a1(b[1]), .a3(a[1]), .saida(A_saida));
  Comparador2BitsIguais u_B (.a0(b[2]), .a2(a[2]), .a1(b[3]), .a3(a[3]), .saida(B_saida));
  and C (Saida, A_saida, B_saida);

  // Notes on the sheet:
  //   Comparador de Igualdade para 4 bits
  //   b2    a2    b3    a3
  //   b0    a0    a1    b1
  //   x1
  //   x2
endmodule

// Iguais
module Comparador2BitsIguais (
  input  a0,
  input  a2,
  input  a1,
  input  a3,
  output saida
);

  wire A_out, B_out;

  xnor A (A_out, a0, a2);
  xnor B (B_out, a1, a3);
  and C (saida, A_out, B_out);

  // Notes on the sheet:
  //   x0
  //   x1
endmodule
