// Logisim project Exemplo0024.circ as structural Verilog: 3 circuits, main circuit main
module main (
  input  [3:0] a,
  input  [3:0] b,
  output Saida
);

  comparador4BitsDiferentes comparador4bitsdiferentes_1 (
    .a(a[0]), .b(a[1]), .c(a[2]), .d(a[3]), .e(b[0]), .f(b[1]), .g(b[2]), .h(b[3]), .Saida(Saida));

  // Notes on the sheet:
  //   Comparador da Diferenca para 4 Bits
endmodule

// Dif
module comparador2BitsDiferentes (
  input  a,
  input  b,
  input  c,
  input  d,
  output Saida
);

  wire A_out, B_out, C_out, D_out, E_out, F_out, G_out, H_out, I_out, J_out;

  xor u_A (A_out, c, d);
  xor u_D (D_out, b, a);
  xor E (E_out, a, c);
  xor F (F_out, b, d);
  and G (G_out, A_out, B_out);
  xnor u_B (B_out, a, b);
  xnor u_C (C_out, d, c);
  and H (H_out, C_out, D_out);
  and I (I_out, E_out, F_out);
  or J (J_out, G_out, H_out);
  or K (Saida, J_out, I_out);

  // Notes on the sheet:
  //   c
  //   d
  //   a
  //   b
  //   c
  //   d
  //   a
  //   b
  //   a
  //   c
  //   d
  //   b
  //   x0
  //   y0
  //   x1
  //   x2
  //   y1
  //   x3
  //   x4
  //   s1
  //   x5
  //   s0
endmodule

// 4 Bits
module comparador4BitsDiferentes (
  input  a,
  input  b,
  input  c,
  input  d,
  input  e,
  input  f,
  input  g,
  input  h,
  output Saida
);

  wire A_saida, B_saida;

  comparador2BitsDiferentes u_A (.a(a), .b(b), .c(e), .d(f), .Saida(A_saida));
  comparador2BitsDiferentes u_B (.a(c), .b(d), .c(g), .d(h), .Saida(B_saida));
  or u_C (Saida, A_saida, B_saida);

  // Notes on the sheet:
  //   s0
  //   s1
endmodule
