// Logisim project Exemplo0025.circ as structural Verilog: 5 circuits, main circuit main
module main (
  input  [3:0] a,
  output Carry_Out,
  output [3:0] Saida
);

  complemento2_4bits complemento2_4bits_1 (
    .Carry_Out(Carry_Out), .a3(a[3]), .a2(a[2]), .a1(a[1]), .a0(a[0]), .s3(Saida[3]), .s2(Saida[2]),
    .s1(Saida[1]), .s0(Saida[0]));

  // Notes on the sheet:
  //   Complemento de 2 para 4 Bits
endmodule

// COMP2
module complemento2_4bits (
  input  a3,
  input  a2,
  input  a1,
  input  a0,
  output Carry_Out,
  output s3,
  output s2,
  output s1,
  output s0
);

  wire A_carry_out, B_carry_out, complemento1_4bits_1_s0, complemento1_4bits_1_s1, complemento1_4bits_1_s2,
       complemento1_4bits_1_s3, somadorde1_1_carry_out;

  halfAdder C (.Carry_out(Carry_Out), .a(complemento1_4bits_1_s3), .saida(s3), .b(B_carry_out));
  halfAdder B (.Carry_out(B_carry_out), .a(complemento1_4bits_1_s2), .saida(s2), .b(A_carry_out));
  complemento1_4Bits complemento1_4bits_1 (
    .a0(a0), .a1(a1), .a2(a2), .a3(a3), .s0(complemento1_4bits_1_s0), .s1(complemento1_4bits_1_s1),
    .s2(complemento1_4bits_1_s2), .s3(complemento1_4bits_1_s3));
  halfAdder A (.Carry_out(A_carry_out), .a(complemento1_4bits_1_s1), .saida(s1), .b(somadorde1_1_carry_out));
  somadorDe1 somadorde1_1 (.Carry_out(somadorde1_1_carry_out), .a(complemento1_4bits_1_s0), .saida(s0));

  // Notes on the sheet:
  //   x3
  //   x2
  //   c2
  //   x1
  //   c1
  //   x0
  //   c0
endmodule

// ADD1
module somadorDe1 (
  input  a,
  output Carry_out,
  output saida
);

  wire C_out, N0_out;

  and u_A (Carry_out, a, C_out);
  xor B (saida, a, C_out);
  not N0 (N0_out, a);
  or C (C_out, N0_out, a);

  // Notes on the sheet:
  //   a
  //   x2
  //   a
  //   x2
  //   x1
  //   a
  //   x2
  //   a
endmodule

// H.A.
module halfAdder (
  input  a,
  input  b,
  output Carry_out,
  output saida
);

  and u_A (Carry_out, a, b);
  xor u_B (saida, a, b);
endmodule

// COMP1
module complemento1_4Bits (
  input  a0,
  input  a1,
  input  a2,
  input  a3,
  output s0,
  output s1,
  output s2,
  output s3
);

  assign {s3, s2, s1, s0} = ~{a3, a2, a1, a0};  // NOT_Gate not_1, 4 bits wide
endmodule
