// Logisim project Exemplo0026.circ as structural Verilog: 10 circuits, main circuit main
module main (
  input  [3:0] a,
  input  [3:0] b,
  input  Switch,
  output Carry_Out,
  output [3:0] Saida
);

  algebrico001 algebrico001_1 (.x(Carry_Out), .a(a), .b(b), .Saida(Saida), .Switch(Switch));

  // Notes on the sheet:
  //   Somador Algebrico de 4 Bits
  //   Legenda Switch:
  //   1 - Subtracao
  //   0 - Adicao
endmodule

module fullAdder (
  input  Carry_In,
  input  a,
  input  b,
  output s,
  output Carry_Out
);

  wire A_carry_out, A_saida, B_carry_out;

  or C (Carry_Out, A_carry_out, B_carry_out);
  halfAdder u_A (.Carry_out(A_carry_out), .a(Carry_In), .saida(A_saida), .b(a));
  halfAdder u_B (.Carry_out(B_carry_out), .a(A_saida), .saida(s), .b(b));

  // Notes on the sheet:
  //   Carry Out
  //   s0
  //   s1
  //   saida
  //   c0
endmodule

// H.A.
module halfAdder (
  input  a,
  input  b,
  output Carry_out,
  output saida
);

  and u_A (Carry_out, a, b);
  xor u_B (saida, a, b);
endmodule

module complemento1_4bits (
  input  a0,
  input  a1,
  input  a2,
  input  a3,
  output s0,
  output s1,
  output s2,
  output s3
);

  assign {s3, s2, s1, s0} = ~{a3, a2, a1, a0};  // NOT_Gate not_1, 4 bits wide
endmodule

// COMP2
module complemento2_4bits (
  input  a3,
  input  a2,
  input  a1,
  input  a0,
  output Carry_Out,
  output s3,
  output s2,
  output s1,
  output s0
);

  wire A_carry_out, B_carry_out, complemento1_4bits_1_s0, complemento1_4bits_1_s1, complemento1_4bits_1_s2,
       complemento1_4bits_1_s3, somadorde1_1_carry_out;

  halfAdder C (.Carry_out(Carry_Out), .a(complemento1_4bits_1_s3), .saida(s3), .b(B_carry_out));
  halfAdder B (.Carry_out(B_carry_out), .a(complemento1_4bits_1_s2), .saida(s2), .b(A_carry_out));
  complemento1_4bits complemento1_4bits_1 (
    .a0(a0), .a1(a1), .a2(a2), .a3(a3), .s0(complemento1_4bits_1_s0), .s1(complemento1_4bits_1_s1),
    .s2(complemento1_4bits_1_s2), .s3(complemento1_4bits_1_s3));
  halfAdder A (.Carry_out(A_carry_out), .a(complemento1_4bits_1_s1), .saida(s1), .b(somadorde1_1_carry_out));
  somadorDe1 somadorde1_1 (.Carry_out(somadorde1_1_carry_out), .a(complemento1_4bits_1_s0), .saida(s0));

  // Notes on the sheet:
  //   x3
  //   x2
  //   c2
  //   x1
  //   c1
  //   x0
  //   c0
endmodule

module somadorDe1 (
  input  a,
  output Carry_out,
  output saida
);

  wire C_out, N0_out;

  and u_A (Carry_out, a, C_out);
  xor B (saida, a, C_out);
  not N0 (N0_out, a);
  or C (C_out, N0_out, a);

  // Notes on the sheet:
  //   a
  //   x2
  //   a
  //   x2
  //   x1
  //   a
  //   x2
  //   a
endmodule

// ADDER
module fullAdder_4Bits (
  input  b3,
  input  b2,
  input  b1,
  input  b0,
  input  a3,
  input  a2,
  input  a1,
  input  a0,
  input  Carry_In,
  output Carry_Out,
  output s3,
  output s2,
  output s1,
  output s0
);

  wire fulladder_2_carry_out, fulladder_3_carry_out, fulladder_4_carry_out;

  fullAdder fulladder_1 (.s(s3), .Carry_In(fulladder_2_carry_out), .Carry_Out(Carry_Out), .a(b3), .b(a3));
  fullAdder fulladder_2 (.s(s2), .Carry_In(fulladder_3_carry_out), .Carry_Out(fulladder_2_carry_out), .a(b2), .b(a2));
  fullAdder fulladder_3 (.s(s1), .Carry_In(fulladder_4_carry_out), .Carry_Out(fulladder_3_carry_out), .a(b1), .b(a1));
  fullAdder fulladder_4 (.s(s0), .Carry_In(Carry_In), .Carry_Out(fulladder_4_carry_out), .a(b0), .b(a0));
endmodule

// S.A.
module algebrico001 (
  input  [3:0] a,
  input  [3:0] b,
  input  Switch,
  output x,
  output [3:0] Saida
);

  wire A_saida, complemento2_4bits_1_carry_out, complemento2_4bits_1_s0, complemento2_4bits_1_s1,
       complemento2_4bits_1_s2, complemento2_4bits_1_s3, fulladder_4bits_1_carry_out, switch_2op_4bits_1_s0,
       switch_2op_4bits_1_s1, switch_2op_4bits_1_s2, switch_2op_4bits_1_s3, zerador_1_saida;

  or C (x, A_saida, fulladder_4bits_1_carry_out);
  zerador u_A (.Saida(A_saida), .a(complemento2_4bits_1_carry_out));
  complemento2_4bits complemento2_4bits_1 (
    .Carry_Out(complemento2_4bits_1_carry_out), .a3(b[3]), .a2(b[2]), .a1(b[1]), .a0(b[0]),
    .s3(complemento2_4bits_1_s3), .s2(complemento2_4bits_1_s2), .s1(complemento2_4bits_1_s1),
    .s0(complemento2_4bits_1_s0));
  switch_2op_4Bits switch_2op_4bits_1 (
    .a3(b[3]), .a2(b[2]), .a1(b[1]), .a0(b[0]), .a3_prime(complemento2_4bits_1_s3),
    .a2_prime(complemento2_4bits_1_s2), .a1_prime(complemento2_4bits_1_s1),
    .a0_prime(complemento2_4bits_1_s0), .s3(switch_2op_4bits_1_s3), .s2(switch_2op_4bits_1_s2),
    .s1(switch_2op_4bits_1_s1), .s0(switch_2op_4bits_1_s0), .Switch(Switch));
  fullAdder_4Bits fulladder_4bits_1 (
    .Carry_Out(fulladder_4bits_1_carry_out), .a3(a[3]), .a2(a[2]), .a1(a[1]), .a0(a[0]),
    .b3(switch_2op_4bits_1_s3), .b2(switch_2op_4bits_1_s2), .b1(switch_2op_4bits_1_s1),
    .b0(switch_2op_4bits_1_s0), .s3(Saida[3]), .s2(Saida[2]), .s1(Saida[1]), .s0(Saida[0]),
    .Carry_In(zerador_1_saida));
  zerador zerador_1 (.Saida(zerador_1_saida), .a(Switch));

  // Notes on the sheet:
  //   Bit desprezivel COMP2
  //   carry out FULL ADDER
  //   carry in
endmodule

// MUX4B
module switch_2op_4Bits (
  input  a3,
  input  a2,
  input  a1,
  input  a0,
  input  a3_prime,
  input  a2_prime,
  input  a1_prime,
  input  a0_prime,
  input  Switch,
  output s3,
  output s2,
  output s1,
  output s0
);

  wire A_out, B_out, C_out, D_out, E_out, F_out, G_out, H_out, N0_out, N1_out, N2_out, N3_out;

  not N3 (N3_out, Switch);
  and G (G_out, a3_prime, Switch);
  and H (H_out, a3, N3_out);
  or L (s3, H_out, G_out);
  not N2 (N2_out, Switch);
  and E (E_out, a2_prime, Switch);
  and F (F_out, a2, N2_out);
  or K (s2, F_out, E_out);
  not N1 (N1_out, Switch);
  and D (D_out, a1, N1_out);
  and C (C_out, a1_prime, Switch);
  or J (s1, D_out, C_out);
  not N0 (N0_out, Switch);
  and A (A_out, a0_prime, Switch);
  and B (B_out, a0, N0_out);
  or I (s0, B_out, A_out);

  // Notes on the sheet:
  //   x3
  //   y7
  //   y6
  //   x2
  //   y5
  //   x1
  //   y4
  //   y3
  //   x0
  //   y1
  //   y2
  //   y0
endmodule

// Zero
module zerador (
  input  a,
  output Saida
);

  wire N_out;

  and u_A (Saida, N_out, a);
  not N (N_out, a);

  // Notes on the sheet:
  //   x0
endmodule
