// Logisim project Exemplo0027.circ as structural Verilog: 7 circuits, main circuit main
module main (
  input  [3:0] a,
  input  [3:0] b,
  input  Switch,
  output Saida
);

  Igualdade_Diferenca igualdade_diferenca_1 (.a(a), .b(b), .Saida(Saida), .Switch(Switch));

  // Notes on the sheet:
  //   Comparador de Igualdade e Diferenca de 4 Bits
  //   Legenda: 
  //   0 - diferentes
  //   1 - iguais
endmodule

// iguais
module Comparador2BitsIguais (
  input  a0,
  input  a2,
  input  a1,
  input  a3,
  output saida
);

  wire A_out, B_out;

  xnor A (A_out, a0, a2);
  xnor B (B_out, a1, a3);
  and C (saida, A_out, B_out);

  // Notes on the sheet:
  //   x0
  //   x1
endmodule

// Iguais
module Comparador4BitsIguais (
  input  a3,
  input  a2,
  input  a1,
  input  a0,
  input  b3,
  input  b2,
  input  b1,
  input  b0,
  output Saida
);

  wire A_saida, B_saida;

  Comparador2BitsIguais A (.a0(b0), .a2(a0), .a1(b1), .a3(a1), .saida(A_saida));
  Comparador2BitsIguais B (.a0(b2), .a2(a2), .a1(b3), .a3(a3), .saida(B_saida));
  and C (Saida, A_saida, B_saida);

  // Notes on the sheet:
  //   b2    a2    b3    a3
  //   b0    a0    a1    b1
  //   x1
  //   x2
endmodule

module Comparador2BitsDiferentes (
  input  a,
  input  b,
  input  c,
  input  d,
  output Saida
);

  wire A_out, B_out, C_out, D_out, E_out, F_out, G_out, H_out, I_out, J_out;

  xor u_A (A_out, c, d);
  xor u_D (D_out, b, a);
  xor E (E_out, a, c);
  xor F (F_out, b, d);
  and G (G_out, A_out, B_out);
  xnor u_B (B_out, a, b);
  xnor u_C (C_out, d, c);
  and H (H_out, C_out, D_out);
  and I (I_out, E_out, F_out);
  or J (J_out, G_out, H_out);
  or K (Saida, J_out, I_out);

  // Notes on the sheet:
  //   c
  //   d
  //   a
  //   b
  //   c
  //   d
  //   a
  //   b
  //   a
  //   c
  //   d
  //   b
  //   x0
  //   y0
  //   x1
  //   x2
  //   y1
  //   x3
  //   x4
  //   s1
  //   x5
  //   s0
endmodule

// Diferentes
module Comparador4BitsDiferentes (
  input  a,
  input  b,
  input  c,
  input  d,
  input  e,
  input  f,
  input  g,
  input  h,
  output Saida
);

  wire comparador2bitsdiferentes_1_saida, comparador2bitsdiferentes_2_saida;

  Comparador2BitsDiferentes comparador2bitsdiferentes_1 (
    .a(a), .b(b), .c(e), .d(f), .Saida(comparador2bitsdiferentes_1_saida));
  Comparador2BitsDiferentes comparador2bitsdiferentes_2 (
    .a(c), .b(d), .c(g), .d(h), .Saida(comparador2bitsdiferentes_2_saida));
  or u_C (Saida, comparador2bitsdiferentes_1_saida, comparador2bitsdiferentes_2_saida);

  // Notes on the sheet:
  //   s0
  //   s1
endmodule

// I.D.
module Igualdade_Diferenca (
  input  [3:0] a,
  input  [3:0] b,
  input  Switch,
  output Saida
);

  wire comparador4bitsdiferentes_1_saida, comparador4bitsiguais_1_saida;

  Comparador4BitsIguais comparador4bitsiguais_1 (
    .a3(a[3]), .a2(a[2]), .a1(a[1]), .a0(a[0]), .b3(b[3]), .b2(b[2]), .b1(b[1]), .b0(b[0]),
    .Saida(comparador4bitsiguais_1_saida));
  Comparador4BitsDiferentes comparador4bitsdiferentes_1 (
    .a(a[3]), .b(a[2]), .c(a[1]), .d(a[0]), .e(b[3]), .f(b[2]), .g(b[1]), .h(b[0]),
    .Saida(comparador4bitsdiferentes_1_saida));
  Switch_2Bits switch_2bits_1 (
    ._1___Selecionado(comparador4bitsiguais_1_saida), ._0___selecionado(comparador4bitsdiferentes_1_saida),
    .Saida(Saida), .switch(Switch));

  // Notes on the sheet:
  //   x0
  //   x1
  //   Legenda: 
  //   1 - iguais
  //   0 - diferentes
endmodule

// MUX
module Switch_2Bits (
  input  _0___selecionado,
  input  _1___Selecionado,
  input  switch,
  output Saida
);

  wire A_out, B_out, N_out;

  not N (N_out, switch);
  and B (B_out, _0___selecionado, N_out);
  and A (A_out, _1___Selecionado, switch);
  or C (Saida, A_out, B_out);

  // Notes on the sheet:
  //   a
  //   y1
  //   b
  //   sw
  //   x0
  //   y0
endmodule
