// Logisim project Exercicio01.circ as structural Verilog: 1 circuit, main circuit main
module main (
  input  [5:0] CarryIn,
  input  [5:0] a,
  input  [5:0] b,
  output [5:0] Soma,
  output [5:0] Carry_Out
);

  wire [5:0] and_1_out, and_2_out, and_3_out, and_4_out, and_5_out, not_1_out, not_2_out, not_3_out,
       or_1_out, undriven, xor_1_out, xor_2_out;

  assign xor_1_out = a ^ b;  // XOR_Gate xor_1, 6 bits wide
  assign not_1_out = ~xor_2_out;  // NOT_Gate not_1, 6 bits wide
  assign xor_2_out = a ^ b;  // XOR_Gate xor_2, 6 bits wide
  assign and_1_out = a & b;  // AND_Gate and_1, 6 bits wide
  assign or_1_out = a | b;  // OR_Gate or_1, 6 bits wide
  assign not_2_out = ~CarryIn;  // NOT_Gate not_2, 6 bits wide
  assign not_3_out = ~CarryIn;  // NOT_Gate not_3, 6 bits wide
  assign and_2_out = xor_1_out & not_2_out;  // AND_Gate and_2, 6 bits wide
  assign and_3_out = undriven & undriven & CarryIn & not_1_out;  // AND_Gate and_3, 6 bits wide
  assign and_4_out = and_1_out & not_3_out & not_3_out;  // AND_Gate and_4, 6 bits wide
  assign and_5_out = or_1_out & CarryIn;  // AND_Gate and_5, 6 bits wide
  assign Soma = and_2_out | and_3_out;  // OR_Gate or_2, 6 bits wide
  assign Carry_Out = and_4_out | and_5_out;  // OR_Gate or_3, 6 bits wide
endmodule
