// Logisim project guia04Exemplo0021(2).circ as structural Verilog: 2 circuits, main circuit main
module main (
  input  a,
  input  b,
  input  carry,
  output s1,
  output s0
);

  wire and1_out, and2_out, xor1_out;

  and and1 (and1_out, a, b);
  xor xor1 (xor1_out, a, b);
  or or1 (s1, and1_out, and2_out);
  and and2 (and2_out, carry, xor1_out);
  xor xor2 (s0, carry, xor1_out);
endmodule

module SysFA4bits (
  input  a0,
  input  a1,
  input  a2,
  input  a3,
  input  b0,
  input  b1,
  input  b2,
  input  b3,
  input  c,
  output s0,
  output s1,
  output s2,
  output s3,
  output s4
);

  wire ad1_s1, ad2_s1, ad3_s1;

  main ad1 (.a(a0), .b(b0), .carry(c), .s1(ad1_s1), .s0(s0));
  main ad2 (.a(a1), .b(b1), .carry(ad1_s1), .s1(ad2_s1), .s0(s1));
  main ad3 (.a(a2), .b(b2), .carry(ad2_s1), .s1(ad3_s1), .s0(s2));
  main ad4 (.a(a3), .b(b3), .carry(ad3_s1), .s1(s4), .s0(s3));
endmodule
