// Logisim project guia04Exemplo0021.circ as structural Verilog: 2 circuits, main circuit main
module main (
  input  a,
  input  b,
  input  carry,
  output out_4,
  output out_5
);

  wire and1_out, and2_out, xor1_out;

  and and1 (and1_out, a, b);
  xor xor1 (xor1_out, a, b);
  or or_1 (out_4, and1_out, and2_out);
  and and2 (and2_out, carry, xor1_out);
  xor xor2 (out_5, carry, xor1_out);
endmodule

module fa (
  input  a0,
  input  a1,
  input  a2,
  input  a3,
  input  b0,
  input  b1,
  input  b2,
  input  b3,
  input  c,
  output s0,
  output s1,
  output s2,
  output s3,
  output s4
);

  wire main_1_out_4, main_2_out_4, main_3_out_4;

  main main_1 (.a(a0), .b(b0), .carry(c), .out_4(main_1_out_4), .out_5(s0));
  main main_2 (.a(a1), .b(b1), .carry(main_1_out_4), .out_4(main_2_out_4), .out_5(s1));
  main main_3 (.a(a2), .b(b2), .carry(main_2_out_4), .out_4(main_3_out_4), .out_5(s2));
  main main_4 (.a(a3), .b(b3), .carry(main_3_out_4), .out_4(s4), .out_5(s3));
endmodule
