// Logisim project guia04Exemplo0024.circ as structural Verilog: 1 circuit, main circuit main
module main (
  input  in_1,
  input  in_2,
  input  in_3,
  input  in_4,
  input  in_5,
  input  in_6,
  input  in_7,
  input  in_8,
  output S
);

  wire xor_1_out, xor_2_out, xor_3_out, xor_4_out;

  xor xor_1 (xor_1_out, in_1, in_5);
  xor xor_2 (xor_2_out, in_2, in_6);
  xor xor_3 (xor_3_out, in_3, in_7);
  xor xor_4 (xor_4_out, in_4, in_8);
  and and_1 (S, xor_1_out, xor_2_out, xor_3_out, xor_4_out);
endmodule
