// Logisim project exemplo21.circ as structural Verilog: 1 circuit, main circuit main
module main (
  input  in_1,
  input  in_2,
  input  in_3,
  input  in_4,
  input  in_5,
  input  in_6,
  input  in_7,
  input  in_8,
  input  in_9,
  output out_10,
  output out_11,
  output out_12,
  output out_13,
  output out_14,
  output out_15,
  output out_16,
  output out_17,
  output out_18
);

  wire and_1_out, and_2_out, and_3_out, and_4_out, and_5_out, and_6_out, and_7_out, and_8_out, xor_1_out,
       xor_3_out, xor_5_out, xor_7_out;

  xor xor_1 (xor_1_out, in_1, in_2);
  and and_1 (and_1_out, xor_1_out, in_9);
  and and_2 (and_2_out, in_2, in_1);
  xor xor_2 (out_14, xor_1_out, in_9);
  or or_1 (out_10, and_1_out, and_2_out);
  xor xor_3 (xor_3_out, in_3, in_4);
  and and_3 (and_3_out, xor_3_out, out_10);
  and and_4 (and_4_out, in_4, in_3);
  xor xor_4 (out_15, xor_3_out, out_10);
  or or_2 (out_13, and_3_out, and_4_out);
  xor xor_5 (xor_5_out, in_5, in_6);
  xor xor_6 (out_16, xor_5_out, out_13);
  and and_5 (and_5_out, xor_5_out, out_13);
  and and_6 (and_6_out, in_6, in_5);
  or or_3 (out_12, and_5_out, and_6_out);
  xor xor_7 (xor_7_out, in_7, in_8);
  and and_7 (and_7_out, xor_7_out, out_12);
  and and_8 (and_8_out, in_8, in_7);
  xor xor_8 (out_17, xor_7_out, out_12);
  or or_4 (out_11, and_7_out, and_8_out);

  assign out_18 = out_11;
endmodule
