// Logisim project exemplo22.circ as structural Verilog: 1 circuit, main circuit main
module main (
  input  vem_um,
  input  primeiro_numero,
  input  in_3,
  input  in_4,
  input  in_5,
  input  in_6,
  input  segundo_numero,
  input  in_8,
  input  in_9,
  output out_10,
  output out_11,
  output out_12,
  output out_13,
  output out_14,
  output out_15,
  output out_16,
  output out_17,
  output bit_de_sinal,
  output out_19,
  output resultado,
  output out_21,
  output out_22
);

  wire and_1_out, and_2_out, and_3_out, and_4_out, and_5_out, and_6_out, and_7_out, and_8_out, not_1_out,
       not_2_out, not_3_out, not_4_out, not_5_out, not_6_out, not_7_out, not_8_out, xor_1_out, xor_3_out,
       xor_5_out, xor_7_out;

  not not_1 (not_1_out, primeiro_numero);
  and and_1 (and_1_out, not_1_out, in_6);
  xor xor_1 (xor_1_out, primeiro_numero, in_6);
  xor xor_2 (out_13, vem_um, xor_1_out);
  not not_2 (not_2_out, xor_1_out);
  and and_2 (and_2_out, vem_um, not_2_out);
  or or_1 (out_17, and_2_out, and_1_out);
  not not_3 (not_3_out, in_3);
  xor xor_3 (xor_3_out, in_3, segundo_numero);
  and and_3 (and_3_out, not_3_out, segundo_numero);
  xor xor_4 (out_12, out_17, xor_3_out);
  not not_4 (not_4_out, xor_3_out);
  and and_4 (and_4_out, out_17, not_4_out);
  or or_2 (out_16, and_4_out, and_3_out);
  not not_5 (not_5_out, in_4);
  xor xor_5 (xor_5_out, in_4, in_8);
  and and_5 (and_5_out, not_5_out, in_8);
  not not_6 (not_6_out, xor_5_out);
  xor xor_6 (out_11, out_16, xor_5_out);
  and and_6 (and_6_out, out_16, not_6_out);
  or or_3 (out_15, and_6_out, and_5_out);
  not not_7 (not_7_out, in_5);
  xor xor_7 (xor_7_out, in_5, in_9);
  and and_7 (and_7_out, not_7_out, in_9);
  xor xor_8 (out_10, out_15, xor_7_out);
  not not_8 (not_8_out, xor_7_out);
  and and_8 (and_8_out, out_15, not_8_out);
  or or_4 (bit_de_sinal, and_8_out, and_7_out);

  assign out_14 = bit_de_sinal;
  assign out_19 = out_13;
  assign out_21 = out_11;
  assign out_22 = out_10;
  assign resultado = out_12;

  // Notes on the sheet:
  //   Lucas Siqueira Chagas - 380783
endmodule
