// Logisim project exemplo25.circ as structural Verilog: 1 circuit, main circuit main
module main (
  input  in_1,
  input  in_2,
  input  in_3,
  input  in_4,
  input  mais_1,
  output out_6,
  output out_7,
  output out_8,
  output out_9,
  output out_10,
  output out_11,
  output out_12,
  output out_13,
  output out_14
);

  wire and_2_out, and_3_out, and_4_out;

  and and_1 (out_6, out_7, and_2_out);
  and and_2 (and_2_out, out_9, and_3_out);
  and and_3 (and_3_out, out_11, and_4_out);
  and and_4 (and_4_out, out_14, mais_1);
  not not_1 (out_7, in_1);
  not not_2 (out_9, in_2);
  not not_3 (out_11, in_3);
  not not_4 (out_14, in_4);
  xor xor_1 (out_13, out_14, mais_1);
  xor xor_2 (out_8, out_7, and_2_out);
  xor xor_3 (out_10, out_9, and_3_out);
  xor xor_4 (out_12, out_11, and_4_out);

  // Notes on the sheet:
  //   entradas - byte
  //   lucas siqueira chagas - 380783
  //   exemplo 25
  //   saidas
endmodule
