// Logisim project Circuitos.circ as structural Verilog: 11 circuits, main circuit FullAdder
// FAx4
module Exemplo0031 (
  input  [3:0] a,
  input  [3:0] b,
  input  Carry_in,
  output Carry_out,
  output [3:0] Saida
);

  wire fulladder_1_carry_out, fulladder_2_carry_out, fulladder_3_carry_out, fulladder_4_carry_out;
  wire [3:0] xor_2_out;

  xor xor_1 (Carry_out, Carry_in, fulladder_2_carry_out);
  FullAdder fulladder_1 (
    .carry_in(fulladder_3_carry_out), .carry_out(fulladder_1_carry_out), .a(a[2]), .b(xor_2_out[2]),
    .s(Saida[2]));
  FullAdder fulladder_2 (
    .carry_in(fulladder_1_carry_out), .carry_out(fulladder_2_carry_out), .a(a[3]), .b(xor_2_out[3]),
    .s(Saida[3]));
  FullAdder fulladder_3 (
    .carry_in(fulladder_4_carry_out), .carry_out(fulladder_3_carry_out), .a(a[1]), .b(xor_2_out[1]),
    .s(Saida[1]));
  assign xor_2_out = b ^ {4{Carry_in}};  // XOR_Gate xor_2, 4 bits wide
  FullAdder fulladder_4 (
    .carry_in(Carry_in), .carry_out(fulladder_4_carry_out), .a(a[0]), .b(xor_2_out[0]), .s(Saida[0]));

  // Notes on the sheet:
  //   Exemplo0031 - Bruno Cezar Andrade Viallet - 396679
endmodule

module Exemplo0032 (
  input  [3:0] a,
  input  [3:0] b,
  input  Carry_in,
  output Carry_out,
  output Equals_0,
  output [3:0] Saida
);

  wire equals_0_1_out_2, equals_0_2_out_2, equals_0_3_out_2, equals_0_4_out_2, fulladder_1_carry_out,
       fulladder_2_carry_out, fulladder_3_carry_out, fulladder_4_carry_out;
  wire [3:0] xor_2_out;

  xor xor_1 (Carry_out, Carry_in, fulladder_2_carry_out);
  FullAdder fulladder_1 (
    .carry_in(fulladder_3_carry_out), .carry_out(fulladder_1_carry_out), .a(a[2]), .b(xor_2_out[2]),
    .s(Saida[2]));
  FullAdder fulladder_2 (
    .carry_in(fulladder_1_carry_out), .carry_out(fulladder_2_carry_out), .a(a[3]), .b(xor_2_out[3]),
    .s(Saida[3]));
  FullAdder fulladder_3 (
    .carry_in(fulladder_4_carry_out), .carry_out(fulladder_3_carry_out), .a(a[1]), .b(xor_2_out[1]),
    .s(Saida[1]));
  assign xor_2_out = b ^ {4{Carry_in}};  // XOR_Gate xor_2, 4 bits wide
  FullAdder fulladder_4 (
    .carry_in(Carry_in), .carry_out(fulladder_4_carry_out), .a(a[0]), .b(xor_2_out[0]), .s(Saida[0]));
  Equals_0 equals_0_1 (.in_1(Saida[0]), .out_2(equals_0_1_out_2));
  Equals_0 equals_0_2 (.in_1(Saida[1]), .out_2(equals_0_2_out_2));
  Equals_0 equals_0_3 (.in_1(Saida[2]), .out_2(equals_0_3_out_2));
  Equals_0 equals_0_4 (.in_1(Saida[3]), .out_2(equals_0_4_out_2));
  and and_1 (Equals_0, equals_0_1_out_2, equals_0_2_out_2, equals_0_3_out_2, equals_0_4_out_2);

  // Notes on the sheet:
  //   Exemplo0032 - Bruno Cezar Andrade Viallet - 396679
endmodule

module Exemplo0033 (
  input  [3:0] a,
  input  [3:0] b,
  input  Carry_in,
  output Carry_out,
  output Teste,
  output [3:0] Saida
);

  wire equals_0_1_out_2, equals_0_2_out_2, equals_0_3_out_2, equals_0_4_out_2, fulladder_1_carry_out,
       fulladder_2_carry_out, fulladder_3_carry_out, fulladder_4_carry_out;
  wire [3:0] plus_minus_1_1_out_3, xor_2_out;

  xor xor_1 (Carry_out, Carry_in, fulladder_2_carry_out);
  Plus_Minus_1 plus_minus_1_1 (._0____1____1____1(1'b0), .a(a), .out_3(plus_minus_1_1_out_3));
  FullAdder fulladder_1 (
    .carry_in(fulladder_3_carry_out), .carry_out(fulladder_1_carry_out), .a(plus_minus_1_1_out_3[2]),
    .b(xor_2_out[2]), .s(Saida[2]));
  FullAdder fulladder_2 (
    .carry_in(fulladder_1_carry_out), .carry_out(fulladder_2_carry_out), .a(plus_minus_1_1_out_3[3]),
    .b(xor_2_out[3]), .s(Saida[3]));
  FullAdder fulladder_3 (
    .carry_in(fulladder_4_carry_out), .carry_out(fulladder_3_carry_out), .a(plus_minus_1_1_out_3[1]),
    .b(xor_2_out[1]), .s(Saida[1]));
  assign xor_2_out = b ^ {4{Carry_in}};  // XOR_Gate xor_2, 4 bits wide
  FullAdder fulladder_4 (
    .carry_in(Carry_in), .carry_out(fulladder_4_carry_out), .a(plus_minus_1_1_out_3[0]), .b(xor_2_out[0]),
    .s(Saida[0]));
  Equals_0 equals_0_1 (.in_1(Saida[0]), .out_2(equals_0_1_out_2));
  Equals_0 equals_0_2 (.in_1(Saida[1]), .out_2(equals_0_2_out_2));
  Equals_0 equals_0_3 (.in_1(Saida[2]), .out_2(equals_0_3_out_2));
  Equals_0 equals_0_4 (.in_1(Saida[3]), .out_2(equals_0_4_out_2));
  and and_1 (Teste, equals_0_1_out_2, equals_0_2_out_2, equals_0_3_out_2, equals_0_4_out_2);

  // Notes on the sheet:
  //   Exemplo0033 - Bruno Cezar Andrade Viallet - 396679
endmodule

module Exemplo0034 (
  input  [3:0] a,
  input  [3:0] b,
  input  Carry_in,
  output Carry_out,
  output Teste,
  output [3:0] Saida
);

  wire equals_0_1_out_2, equals_0_2_out_2, equals_0_3_out_2, equals_0_4_out_2, fulladder_1_carry_out,
       fulladder_2_carry_out, fulladder_3_carry_out, fulladder_4_carry_out;
  wire [3:0] plus_minus_1_1_out_3, xor_2_out;

  xor xor_1 (Carry_out, Carry_in, fulladder_1_carry_out);
  Plus_Minus_1 plus_minus_1_1 (._0____1____1____1(1'b1), .a(a), .out_3(plus_minus_1_1_out_3));
  FullAdder fulladder_1 (
    .carry_in(fulladder_2_carry_out), .carry_out(fulladder_1_carry_out), .a(plus_minus_1_1_out_3[3]),
    .b(xor_2_out[3]), .s(Saida[3]));
  FullAdder fulladder_2 (
    .carry_in(fulladder_3_carry_out), .carry_out(fulladder_2_carry_out), .a(plus_minus_1_1_out_3[2]),
    .b(xor_2_out[2]), .s(Saida[2]));
  FullAdder fulladder_3 (
    .carry_in(fulladder_4_carry_out), .carry_out(fulladder_3_carry_out), .a(plus_minus_1_1_out_3[1]),
    .b(xor_2_out[1]), .s(Saida[1]));
  assign xor_2_out = b ^ {4{Carry_in}};  // XOR_Gate xor_2, 4 bits wide
  FullAdder fulladder_4 (
    .carry_in(Carry_in), .carry_out(fulladder_4_carry_out), .a(plus_minus_1_1_out_3[0]), .b(xor_2_out[0]),
    .s(Saida[0]));
  Equals_0 equals_0_1 (.in_1(Saida[0]), .out_2(equals_0_1_out_2));
  Equals_0 equals_0_2 (.in_1(Saida[1]), .out_2(equals_0_2_out_2));
  Equals_0 equals_0_3 (.in_1(Saida[2]), .out_2(equals_0_3_out_2));
  Equals_0 equals_0_4 (.in_1(Saida[3]), .out_2(equals_0_4_out_2));
  and and_1 (Teste, equals_0_1_out_2, equals_0_2_out_2, equals_0_3_out_2, equals_0_4_out_2);

  // Notes on the sheet:
  //   Exemplo0034 - Bruno Cezar Andrade Viallet - 396679
endmodule

module Exemplo0035 (
  input  [3:0] a,
  input  [3:0] b,
  output A___B,
  output A___B_2
);

  wire [2:0] exemplo0031_1_saida;

  Exemplo0031 exemplo0031_1 (.Carry_in(1'b1), .a(a), .b(b), .Saida({A___B, exemplo0031_1_saida}));  // open: Carry_out
  not not_1 (A___B_2, A___B);

  // Notes on the sheet:
  //   Exemplo0035 - Bruno Cezar Andrade Viallet - 396679
endmodule

module Exemplo0036 (
  input  [3:0] a,
  input  [3:0] b,
  input  _0____1____1____1,
  input  Carry_in,
  output Overflow,
  output Teste,
  output [3:0] Saida
);

  wire equals_0_1_out_2, equals_0_2_out_2, equals_0_3_out_2, equals_0_4_out_2, fulladder_1_carry_out,
       fulladder_2_carry_out, fulladder_3_carry_out, fulladder_4_carry_out;
  wire [3:0] plus_minus_1_1_out_3, xor_2_out;

  xor xor_1 (Overflow, Carry_in, fulladder_1_carry_out);
  Plus_Minus_1 plus_minus_1_1 (._0____1____1____1(_0____1____1____1), .a(a), .out_3(plus_minus_1_1_out_3));
  FullAdder fulladder_1 (
    .carry_in(fulladder_2_carry_out), .carry_out(fulladder_1_carry_out), .a(plus_minus_1_1_out_3[3]),
    .b(xor_2_out[3]), .s(Saida[3]));
  FullAdder fulladder_2 (
    .carry_in(fulladder_3_carry_out), .carry_out(fulladder_2_carry_out), .a(plus_minus_1_1_out_3[2]),
    .b(xor_2_out[2]), .s(Saida[2]));
  FullAdder fulladder_3 (
    .carry_in(fulladder_4_carry_out), .carry_out(fulladder_3_carry_out), .a(plus_minus_1_1_out_3[1]),
    .b(xor_2_out[1]), .s(Saida[1]));
  assign xor_2_out = b ^ {4{Carry_in}};  // XOR_Gate xor_2, 4 bits wide
  FullAdder fulladder_4 (
    .carry_in(Carry_in), .carry_out(fulladder_4_carry_out), .a(plus_minus_1_1_out_3[0]), .b(xor_2_out[0]),
    .s(Saida[0]));
  Equals_0 equals_0_1 (.in_1(Saida[0]), .out_2(equals_0_1_out_2));
  Equals_0 equals_0_2 (.in_1(Saida[1]), .out_2(equals_0_2_out_2));
  Equals_0 equals_0_3 (.in_1(Saida[2]), .out_2(equals_0_3_out_2));
  Equals_0 equals_0_4 (.in_1(Saida[3]), .out_2(equals_0_4_out_2));
  and and_1 (Teste, equals_0_1_out_2, equals_0_2_out_2, equals_0_3_out_2, equals_0_4_out_2);

  // Notes on the sheet:
  //   Exemplo0036 - Bruno Cezar Andrade Viallet - 396679
endmodule

module Exemplo0037 (
  input  [3:0] a,
  input  [3:0] b,
  input  _0____1____1____1,
  input  Carry_in,
  output Carry_out,
  output Teste,
  output [3:0] Saida
);

  wire equals_0_1_out_2, equals_0_2_out_2, equals_0_3_out_2, equals_0_4_out_2, fulladder_1_carry_out,
       fulladder_2_carry_out, fulladder_3_carry_out, fulladder_4_carry_out;
  wire [3:0] plus_minus_1_1_out_3, xor_2_out;

  xor xor_1 (Carry_out, Carry_in, fulladder_1_carry_out);
  Plus_Minus_1 plus_minus_1_1 (._0____1____1____1(_0____1____1____1), .a(a), .out_3(plus_minus_1_1_out_3));
  FullAdder fulladder_1 (
    .carry_in(fulladder_2_carry_out), .carry_out(fulladder_1_carry_out), .a(plus_minus_1_1_out_3[3]),
    .b(xor_2_out[3]), .s(Saida[3]));
  FullAdder fulladder_2 (
    .carry_in(fulladder_3_carry_out), .carry_out(fulladder_2_carry_out), .a(plus_minus_1_1_out_3[2]),
    .b(xor_2_out[2]), .s(Saida[2]));
  FullAdder fulladder_3 (
    .carry_in(fulladder_4_carry_out), .carry_out(fulladder_3_carry_out), .a(plus_minus_1_1_out_3[1]),
    .b(xor_2_out[1]), .s(Saida[1]));
  assign xor_2_out = b ^ {4{Carry_in}};  // XOR_Gate xor_2, 4 bits wide
  FullAdder fulladder_4 (
    .carry_in(Carry_in), .carry_out(fulladder_4_carry_out), .a(plus_minus_1_1_out_3[0]), .b(xor_2_out[0]),
    .s(Saida[0]));
  Equals_0 equals_0_1 (.in_1(Saida[0]), .out_2(equals_0_1_out_2));
  Equals_0 equals_0_2 (.in_1(Saida[1]), .out_2(equals_0_2_out_2));
  Equals_0 equals_0_3 (.in_1(Saida[2]), .out_2(equals_0_3_out_2));
  Equals_0 equals_0_4 (.in_1(Saida[3]), .out_2(equals_0_4_out_2));
  and and_1 (Teste, equals_0_1_out_2, equals_0_2_out_2, equals_0_3_out_2, equals_0_4_out_2);

  // Notes on the sheet:
  //   Exemplo0037 - Bruno Cezar Andrade Viallet - 396679
endmodule

// T.I
module Equals_0 (
  input  in_1,
  output out_2
);

  nor nor_1 (out_2, in_1, 1'b0);

  // Notes on the sheet:
  //   Bruno Cezar Andrade Viallet - 396679
endmodule

// +/- 1
module Plus_Minus_1 (
  input  [3:0] a,
  input  _0____1____1____1,
  output [3:0] out_3
);

  wire exemplo0031_1_carry_out;

  Exemplo0031 exemplo0031_1 (
    .Carry_out(exemplo0031_1_carry_out), .Carry_in(_0____1____1____1), .a(a), .b(4'b0001), .Saida(out_3));

  // Notes on the sheet:
  //   Bruno Cezar Andrade Viallet - 396679
endmodule

// 4bit F.A
module _4bitFullAdder (
  input  a_3,
  input  a_2,
  input  a_1,
  input  a_0,
  input  b_3,
  input  b_2,
  input  b_1,
  input  b_0,
  input  Carry_in,
  output Carry_out,
  output [3:0] out_11
);

  wire fulladder_2_carry_out, fulladder_3_carry_out, fulladder_4_carry_out;

  FullAdder fulladder_1 (.carry_in(fulladder_2_carry_out), .carry_out(Carry_out), .a(a_3), .b(b_3), .s(out_11[3]));
  FullAdder fulladder_2 (
    .carry_in(fulladder_3_carry_out), .carry_out(fulladder_2_carry_out), .a(a_2), .b(b_2), .s(out_11[2]));
  FullAdder fulladder_3 (
    .carry_in(fulladder_4_carry_out), .carry_out(fulladder_3_carry_out), .a(a_1), .b(b_1), .s(out_11[1]));
  FullAdder fulladder_4 (.carry_in(Carry_in), .carry_out(fulladder_4_carry_out), .a(a_0), .b(b_0), .s(out_11[0]));

  // Notes on the sheet:
  //   Bruno Cezar Andrade Viallet - 396679
endmodule

// F.A
module FullAdder (
  input  a,
  input  b,
  input  carry_in,
  output carry_out,
  output s
);

  wire and_1_out, and_2_out, xor_1_out;

  xor xor_1 (xor_1_out, b, a);
  and and_1 (and_1_out, a, b);
  and and_2 (and_2_out, xor_1_out, carry_in);
  xor xor_2 (s, carry_in, xor_1_out);
  or or_1 (carry_out, and_2_out, and_1_out);

  // Notes on the sheet:
  //   Bruno Cezar Andrade Viallet - 396679
endmodule
