// Logisim project Circuitos.circ as structural Verilog: 10 circuits, main circuit FullAdder
// F.A
module FullAdder (
  input  a,
  input  b,
  input  carry_in,
  output carry_out,
  output s
);

  wire and_1_out, and_2_out, xor_1_out;

  xor xor_1 (xor_1_out, b, a);
  and and_1 (and_1_out, a, b);
  and and_2 (and_2_out, xor_1_out, carry_in);
  xor xor_2 (s, carry_in, xor_1_out);
  or or_1 (carry_out, and_2_out, and_1_out);

  // Notes on the sheet:
  //   Alvaro Henrique de Araujo Rungue - 395487
endmodule

module VerificarSeE0 (
  input  in_1,
  input  in_2,
  input  in_3,
  input  in_4,
  output out_5
);

  wire nor_1_out, nor_2_out, nor_3_out, nor_4_out;

  nor nor_1 (nor_1_out, 1'b0, in_1);
  nor nor_2 (nor_2_out, 1'b0, in_2);
  nor nor_3 (nor_3_out, 1'b0, in_3);
  and and_1 (out_5, nor_1_out, nor_2_out, nor_3_out, nor_4_out);
  nor nor_4 (nor_4_out, 1'b0, in_4);
endmodule

module Soma_Subs (
  input  in_1,
  input  in_2,
  input  in_3,
  input  in_4,
  input  _0___SOMA___1___Substracao,
  output out_6,
  output out_7,
  output out_8,
  output out_9
);

  wire exemplo0031_1_carry_out;

  Exemplo0031 exemplo0031_1 (
    .a_3(in_1), .b_3(1'b0), .a_2(in_2), .b_2(1'b0), .a_1(in_3), .b_1(1'b0), .a_0(in_4), .b_0(1'b1),
    .Carry_out(exemplo0031_1_carry_out), .s_3(out_6), .s_2(out_7), .s_1(out_8), .s_0(out_9),
    .Carry_in(_0___SOMA___1___Substracao));
endmodule

module Exemplo0031 (
  input  a_3,
  input  b_3,
  input  a_2,
  input  b_2,
  input  a_1,
  input  b_1,
  input  a_0,
  input  b_0,
  input  Carry_in,
  output s_3,
  output s_2,
  output s_1,
  output s_0,
  output Carry_out
);

  wire fulladder_1_carry_out, fulladder_2_carry_out, fulladder_3_carry_out, fulladder_4_carry_out, xor_2_out,
       xor_3_out, xor_4_out, xor_5_out;

  xor xor_1 (Carry_out, Carry_in, fulladder_1_carry_out);
  xor xor_2 (xor_2_out, b_3, Carry_in);
  xor xor_3 (xor_3_out, b_2, Carry_in);
  FullAdder fulladder_1 (
    .carry_in(fulladder_3_carry_out), .carry_out(fulladder_1_carry_out), .a(a_3), .b(xor_2_out), .s(s_3));
  xor xor_4 (xor_4_out, b_1, Carry_in);
  FullAdder fulladder_2 (
    .carry_in(fulladder_4_carry_out), .carry_out(fulladder_2_carry_out), .a(a_1), .b(xor_4_out), .s(s_1));
  FullAdder fulladder_3 (
    .carry_in(fulladder_2_carry_out), .carry_out(fulladder_3_carry_out), .a(a_2), .b(xor_3_out), .s(s_2));
  xor xor_5 (xor_5_out, b_0, Carry_in);
  FullAdder fulladder_4 (.carry_in(Carry_in), .carry_out(fulladder_4_carry_out), .a(a_0), .b(xor_5_out), .s(s_0));

  // Notes on the sheet:
  //   Alvaro Henrique de Araujo Rungue - 395487
endmodule

module Exemplo0032 (
  input  a_3,
  input  b_3,
  input  a_2,
  input  b_2,
  input  a_1,
  input  b_1,
  input  a_0,
  input  b_0,
  input  Carry_in,
  output s_3,
  output s_2,
  output s_1,
  output s_0,
  output Carry_out,
  output out_15
);

  wire fulladder_1_carry_out, fulladder_2_carry_out, fulladder_3_carry_out, fulladder_4_carry_out, xor_2_out,
       xor_3_out, xor_4_out, xor_5_out;

  xor xor_1 (Carry_out, Carry_in, fulladder_1_carry_out);
  xor xor_2 (xor_2_out, b_3, Carry_in);
  xor xor_3 (xor_3_out, b_2, Carry_in);
  FullAdder fulladder_1 (
    .carry_in(fulladder_2_carry_out), .carry_out(fulladder_1_carry_out), .a(a_3), .b(xor_2_out), .s(s_3));
  xor xor_4 (xor_4_out, b_1, Carry_in);
  FullAdder fulladder_2 (
    .carry_in(fulladder_3_carry_out), .carry_out(fulladder_2_carry_out), .a(a_2), .b(xor_3_out), .s(s_2));
  FullAdder fulladder_3 (
    .carry_in(fulladder_4_carry_out), .carry_out(fulladder_3_carry_out), .a(a_1), .b(xor_4_out), .s(s_1));
  VerificarSeE0 verificarsee0_1 (.in_1(s_3), .in_2(s_2), .in_3(s_1), .in_4(s_0), .out_5(out_15));
  xor xor_5 (xor_5_out, b_0, Carry_in);
  FullAdder fulladder_4 (.carry_in(Carry_in), .carry_out(fulladder_4_carry_out), .a(a_0), .b(xor_5_out), .s(s_0));

  // Notes on the sheet:
  //   Alvaro Henrique de Araujo Rungue - 395487
endmodule

module Exemplo0033 (
  input  a_3,
  input  a_2,
  input  a_1,
  input  a_0,
  input  b_3,
  input  b_2,
  input  b_1,
  input  b_0,
  input  Carry_in,
  output s_3,
  output s_2,
  output s_1,
  output s_0,
  output Carry_out,
  output out_15
);

  wire fulladder_1_carry_out, fulladder_2_carry_out, fulladder_3_carry_out, fulladder_4_carry_out,
       soma_subs_1_out_6, soma_subs_1_out_7, soma_subs_1_out_8, soma_subs_1_out_9, xor_2_out, xor_3_out,
       xor_4_out, xor_5_out;

  xor xor_1 (Carry_out, Carry_in, fulladder_1_carry_out);
  xor xor_2 (xor_2_out, b_3, Carry_in);
  FullAdder fulladder_1 (
    .carry_in(fulladder_2_carry_out), .carry_out(fulladder_1_carry_out), .a(soma_subs_1_out_6),
    .b(xor_2_out), .s(s_3));
  Soma_Subs soma_subs_1 (
    ._0___SOMA___1___Substracao(1'b0), .in_1(a_3), .in_2(a_2), .in_3(a_1), .in_4(a_0),
    .out_6(soma_subs_1_out_6), .out_7(soma_subs_1_out_7), .out_8(soma_subs_1_out_8), .out_9(soma_subs_1_out_9));
  xor xor_3 (xor_3_out, b_1, Carry_in);
  xor xor_4 (xor_4_out, b_2, Carry_in);
  FullAdder fulladder_2 (
    .carry_in(fulladder_3_carry_out), .carry_out(fulladder_2_carry_out), .a(soma_subs_1_out_7),
    .b(xor_4_out), .s(s_2));
  VerificarSeE0 verificarsee0_1 (.in_1(s_3), .in_2(s_2), .in_3(s_1), .in_4(s_0), .out_5(out_15));
  xor xor_5 (xor_5_out, b_0, Carry_in);
  FullAdder fulladder_3 (
    .carry_in(fulladder_4_carry_out), .carry_out(fulladder_3_carry_out), .a(soma_subs_1_out_8),
    .b(xor_3_out), .s(s_1));
  FullAdder fulladder_4 (
    .carry_in(Carry_in), .carry_out(fulladder_4_carry_out), .a(soma_subs_1_out_9), .b(xor_5_out), .s(s_0));

  // Notes on the sheet:
  //   Alvaro Henrique de Araujo Rungue - 395487
endmodule

module Exemplo0034 (
  input  a_3,
  input  a_2,
  input  a_1,
  input  a_0,
  input  b_3,
  input  b_2,
  input  b_1,
  input  b_0,
  input  Carry_in,
  output s_3,
  output s_2,
  output s_1,
  output s_0,
  output Carry_out,
  output out_15
);

  wire fulladder_1_carry_out, fulladder_2_carry_out, fulladder_3_carry_out, fulladder_4_carry_out,
       soma_subs_1_out_6, soma_subs_1_out_7, soma_subs_1_out_8, soma_subs_1_out_9, xor_2_out, xor_3_out,
       xor_4_out, xor_5_out;

  xor xor_1 (Carry_out, Carry_in, fulladder_1_carry_out);
  xor xor_2 (xor_2_out, b_3, Carry_in);
  FullAdder fulladder_1 (
    .carry_in(fulladder_2_carry_out), .carry_out(fulladder_1_carry_out), .a(soma_subs_1_out_6),
    .b(xor_2_out), .s(s_3));
  Soma_Subs soma_subs_1 (
    ._0___SOMA___1___Substracao(1'b1), .in_1(a_3), .in_2(a_2), .in_3(a_1), .in_4(a_0),
    .out_6(soma_subs_1_out_6), .out_7(soma_subs_1_out_7), .out_8(soma_subs_1_out_8), .out_9(soma_subs_1_out_9));
  xor xor_3 (xor_3_out, b_1, Carry_in);
  xor xor_4 (xor_4_out, b_2, Carry_in);
  FullAdder fulladder_2 (
    .carry_in(fulladder_3_carry_out), .carry_out(fulladder_2_carry_out), .a(soma_subs_1_out_7),
    .b(xor_4_out), .s(s_2));
  VerificarSeE0 verificarsee0_1 (.in_1(s_3), .in_2(s_2), .in_3(s_1), .in_4(s_0), .out_5(out_15));
  xor xor_5 (xor_5_out, b_0, Carry_in);
  FullAdder fulladder_3 (
    .carry_in(fulladder_4_carry_out), .carry_out(fulladder_3_carry_out), .a(soma_subs_1_out_8),
    .b(xor_3_out), .s(s_1));
  FullAdder fulladder_4 (
    .carry_in(Carry_in), .carry_out(fulladder_4_carry_out), .a(soma_subs_1_out_9), .b(xor_5_out), .s(s_0));

  // Notes on the sheet:
  //   Alvaro Henrique de Araujo Rungue - 395487
endmodule

module Exemplo0035 (
  input  A,
  input  in_2,
  input  in_3,
  input  in_4,
  input  B,
  input  in_6,
  input  in_7,
  input  in_8,
  output A___B,
  output A___B_2
);

  wire exemplo0031_1_carry_out;

  not not_1 (A___B_2, A___B);
  Exemplo0031 exemplo0031_1 (
    .a_3(A), .b_3(B), .a_2(in_2), .b_2(in_6), .a_1(in_3), .b_1(in_7), .a_0(in_4), .b_0(in_8),
    .Carry_out(exemplo0031_1_carry_out), .s_3(A___B), .Carry_in(1'b1));  // open: s_2, s_1, s_0
endmodule

module Exemplo0036 (
  input  a_3,
  input  b_3,
  input  a_2,
  input  b_2,
  input  a_1,
  input  b_1,
  input  a_0,
  input  b_0,
  input  Carry_in,
  output s_3,
  output s_2,
  output s_1,
  output s_0,
  output Overflow,
  output out_15
);

  wire fulladder_1_carry_out, fulladder_2_carry_out, fulladder_3_carry_out, fulladder_4_carry_out, xor_2_out,
       xor_3_out, xor_4_out, xor_5_out;

  xor xor_1 (Overflow, Carry_in, fulladder_1_carry_out);
  xor xor_2 (xor_2_out, b_3, Carry_in);
  xor xor_3 (xor_3_out, b_2, Carry_in);
  FullAdder fulladder_1 (
    .carry_in(fulladder_3_carry_out), .carry_out(fulladder_1_carry_out), .a(a_3), .b(xor_2_out), .s(s_3));
  xor xor_4 (xor_4_out, b_1, Carry_in);
  FullAdder fulladder_2 (
    .carry_in(fulladder_4_carry_out), .carry_out(fulladder_2_carry_out), .a(a_1), .b(xor_4_out), .s(s_1));
  FullAdder fulladder_3 (
    .carry_in(fulladder_2_carry_out), .carry_out(fulladder_3_carry_out), .a(a_2), .b(xor_3_out), .s(s_2));
  VerificarSeE0 verificarsee0_1 (.in_1(s_3), .in_2(s_2), .in_3(s_1), .in_4(s_0), .out_5(out_15));
  xor xor_5 (xor_5_out, b_0, Carry_in);
  FullAdder fulladder_4 (.carry_in(Carry_in), .carry_out(fulladder_4_carry_out), .a(a_0), .b(xor_5_out), .s(s_0));

  // Notes on the sheet:
  //   Alvaro Henrique de Araujo Rungue - 395487
endmodule

module Exemplo0037 (
  input  a_3,
  input  a_2,
  input  a_1,
  input  a_0,
  input  Operador,
  input  b_3,
  input  b_2,
  input  b_1,
  input  b_0,
  input  Carry_in,
  output s_3,
  output s_2,
  output s_1,
  output s_0,
  output Carry_out,
  output out_16
);

  wire fulladder_1_carry_out, fulladder_2_carry_out, fulladder_3_carry_out, fulladder_4_carry_out,
       soma_subs_1_out_6, soma_subs_1_out_7, soma_subs_1_out_8, soma_subs_1_out_9, xor_2_out, xor_3_out,
       xor_4_out, xor_5_out;

  xor xor_1 (Carry_out, Carry_in, fulladder_1_carry_out);
  xor xor_2 (xor_2_out, b_3, Carry_in);
  FullAdder fulladder_1 (
    .carry_in(fulladder_2_carry_out), .carry_out(fulladder_1_carry_out), .a(soma_subs_1_out_6),
    .b(xor_2_out), .s(s_3));
  Soma_Subs soma_subs_1 (
    ._0___SOMA___1___Substracao(Operador), .in_1(a_3), .in_2(a_2), .in_3(a_1), .in_4(a_0),
    .out_6(soma_subs_1_out_6), .out_7(soma_subs_1_out_7), .out_8(soma_subs_1_out_8), .out_9(soma_subs_1_out_9));
  xor xor_3 (xor_3_out, b_1, Carry_in);
  xor xor_4 (xor_4_out, b_2, Carry_in);
  FullAdder fulladder_2 (
    .carry_in(fulladder_3_carry_out), .carry_out(fulladder_2_carry_out), .a(soma_subs_1_out_7),
    .b(xor_4_out), .s(s_2));
  VerificarSeE0 verificarsee0_1 (.in_1(s_3), .in_2(s_2), .in_3(s_1), .in_4(s_0), .out_5(out_16));
  xor xor_5 (xor_5_out, b_0, Carry_in);
  FullAdder fulladder_3 (
    .carry_in(fulladder_4_carry_out), .carry_out(fulladder_3_carry_out), .a(soma_subs_1_out_8),
    .b(xor_3_out), .s(s_1));
  FullAdder fulladder_4 (
    .carry_in(Carry_in), .carry_out(fulladder_4_carry_out), .a(soma_subs_1_out_9), .b(xor_5_out), .s(s_0));

  // Notes on the sheet:
  //   Alvaro Henrique de Araujo Rungue - 395487
endmodule
