// Logisim project Exemplo0033.circ as structural Verilog: 5 circuits, main circuit main
module main (
  input  [5:0] in_1,
  input  [5:0] in_2,
  input  in_3,
  input  [5:0] in_4,
  output Overf,
  output [5:0] out_6
);

  wire [5:0] circuit_1_out_5;

  Exemplo0031 exemplo0031_1 (
    .in_1(in_4), .in_2(circuit_1_out_5), .s0(out_6[5]), .s1(out_6[4]), .s2(out_6[3]), .s3(out_6[2]),
    .s4(out_6[1]), .s5(out_6[0]), .Chave(in_3), .Over(Overf));
  circuit circuit_1 (.out_5(circuit_1_out_5), .in_1(in_3), .in_2(in_1), .in_3(in_2));  // open: out_4

  // Notes on the sheet:
  //   soma = carryIn = 0
  //   subtraçao = carryIn = 1
  //   Exemplo0033 - João Henrique Mendes de Oliveira - 392734
endmodule

module Exemplo0031 (
  input  [5:0] in_1,
  input  [5:0] in_2,
  input  Chave,
  output s0,
  output s1,
  output s2,
  output s3,
  output s4,
  output s5,
  output Over
);

  wire selecionar_1_s1, selecionar_2_s1, selecionar_3_s1, selecionar_4_s1, selecionar_6_s1;

  Selecionar selecionar_1 (.x(in_1[0]), .y(in_2[0]), .C_in(Chave), .Selecionador(Chave), .s0(s0), .s1(selecionar_1_s1));
  Selecionar selecionar_2 (
    .x(in_1[1]), .y(in_2[1]), .C_in(selecionar_1_s1), .Selecionador(Chave), .s0(s1), .s1(selecionar_2_s1));
  Selecionar selecionar_3 (
    .x(in_1[2]), .y(in_2[2]), .C_in(selecionar_2_s1), .Selecionador(Chave), .s0(s2), .s1(selecionar_3_s1));
  Selecionar selecionar_4 (
    .x(in_1[3]), .y(in_2[3]), .C_in(selecionar_3_s1), .Selecionador(Chave), .s0(s3), .s1(selecionar_4_s1));
  Selecionar selecionar_5 (
    .x(in_1[4]), .y(in_2[4]), .C_in(selecionar_4_s1), .Selecionador(Chave), .s0(s4));  // open: s1
  Selecionar selecionar_6 (.x(in_1[5]), .y(in_2[5]), .C_in(Chave), .Selecionador(Chave), .s0(s5), .s1(selecionar_6_s1));
  xor xor_1 (Over, Chave, selecionar_6_s1);
endmodule

module full_adder (
  input  C_in,
  input  x,
  input  y,
  output s0,
  output s1
);

  wire and_1_out, and_2_out, xor_1_out;

  xor xor_1 (xor_1_out, x, y);
  and and_1 (and_1_out, x, y);
  xor xor_2 (s0, C_in, xor_1_out);
  and and_2 (and_2_out, C_in, xor_1_out);
  or or_1 (s1, and_2_out, and_1_out);
endmodule

module Selecionar (
  input  x,
  input  y,
  input  C_in,
  input  Selecionador,
  output s0,
  output s1
);

  wire xor_1_out;

  xor xor_1 (xor_1_out, y, Selecionador);
  full_adder full_adder_1 (.C_in(C_in), .x(x), .y(xor_1_out), .s0(s0), .s1(s1));
endmodule

module circuit (
  input  in_1,
  input  [5:0] in_2,
  input  [5:0] in_3,
  output out_4,
  output [5:0] out_5
);

  Exemplo0031 exemplo0031_1 (
    .in_1(in_3), .in_2(in_2), .s0(out_5[5]), .s1(out_5[4]), .s2(out_5[3]), .s3(out_5[2]), .s4(out_5[1]),
    .s5(out_5[0]), .Chave(in_1), .Over(out_4));
endmodule
