// Logisim project Exemplo0035.circ as structural Verilog: 4 circuits, main circuit main
module main (
  input  [5:0] in_1,
  input  [5:0] in_2,
  input  in_3,
  input  in_4,
  output out_5
);

  wire and_1_out, and_2_out, and_3_out, equal_circuit_1_out_3, greater_circuit_1_out_3, less_circuit_1_out_3,
       not_1_out, not_2_out, not_3_out, not_4_out, or_1_out;

  equal_circuit equal_circuit_1 (.in_1(in_1), .in_2(in_2), .out_3(equal_circuit_1_out_3));
  greater_circuit greater_circuit_1 (.in_1(in_1), .in_2(in_2), .out_3(greater_circuit_1_out_3));
  less_circuit less_circuit_1 (.in_1(in_1), .in_2(in_2), .out_3(less_circuit_1_out_3));
  not not_1 (not_1_out, in_3);
  not not_2 (not_2_out, in_4);
  not not_3 (not_3_out, in_3);
  not not_4 (not_4_out, in_4);
  and and_1 (and_1_out, less_circuit_1_out_3, not_4_out, in_3);
  and and_2 (and_2_out, equal_circuit_1_out_3, not_1_out, not_2_out);
  and and_3 (and_3_out, greater_circuit_1_out_3, in_4, not_3_out);
  or or_1 (or_1_out, and_2_out, and_3_out);
  or or_2 (out_5, or_1_out, and_1_out);

  // Notes on the sheet:
  //   equal
  //   greater
  //   less
  //   Exemplo0035 - João Henrique Mendes de Oliveira - 392734
endmodule

module equal_circuit (
  input  [5:0] in_1,
  input  [5:0] in_2,
  output out_3
);

  wire and_1_out, and_2_out, and_4_out, and_5_out, xnor_1_out, xnor_2_out, xnor_3_out, xnor_4_out,
       xnor_5_out, xnor_6_out;

  xnor xnor_1 (xnor_1_out, in_1[0], in_2[0]);
  and and_1 (and_1_out, xnor_1_out, xnor_2_out);
  xnor xnor_2 (xnor_2_out, in_1[1], in_2[1]);
  and and_2 (and_2_out, and_1_out, and_4_out);
  and and_3 (out_3, and_5_out, and_2_out);
  xnor xnor_3 (xnor_3_out, in_1[2], in_2[2]);
  and and_4 (and_4_out, xnor_3_out, xnor_4_out);
  xnor xnor_4 (xnor_4_out, in_1[3], in_2[3]);
  xnor xnor_5 (xnor_5_out, in_1[4], in_2[4]);
  xnor xnor_6 (xnor_6_out, in_1[5], in_2[5]);
  and and_5 (and_5_out, xnor_5_out, xnor_6_out);
endmodule

module less_circuit (
  input  [5:0] in_1,
  input  [5:0] in_2,
  output out_3
);

  wire and_1_out, and_2_out, and_3_out, and_4_out, and_5_out, and_6_out, not_1_out, not_2_out, not_3_out,
       not_4_out, not_5_out, not_6_out, or_1_out, or_2_out, or_4_out, or_5_out;

  and and_1 (and_1_out, in_1[0], not_1_out);
  not not_1 (not_1_out, in_2[0]);
  or or_1 (or_1_out, and_1_out, and_2_out);
  and and_2 (and_2_out, in_1[1], not_2_out);
  not not_2 (not_2_out, in_2[1]);
  or or_2 (or_2_out, or_1_out, or_4_out);
  or or_3 (out_3, or_5_out, or_2_out);
  and and_3 (and_3_out, in_1[2], not_4_out);
  not not_3 (not_3_out, in_2[3]);
  not not_4 (not_4_out, in_2[2]);
  or or_4 (or_4_out, and_3_out, and_4_out);
  and and_4 (and_4_out, in_1[3], not_3_out);
  not not_5 (not_5_out, in_2[4]);
  and and_5 (and_5_out, in_1[5], not_6_out);
  and and_6 (and_6_out, in_1[4], not_5_out);
  not not_6 (not_6_out, in_2[5]);
  or or_5 (or_5_out, and_6_out, and_5_out);
endmodule

module greater_circuit (
  input  [5:0] in_1,
  input  [5:0] in_2,
  output out_3
);

  wire and_1_out, and_2_out, and_3_out, and_4_out, and_5_out, and_6_out, not_1_out, not_2_out, not_3_out,
       not_4_out, not_5_out, not_6_out, or_1_out, or_2_out, or_4_out, or_5_out;

  not not_1 (not_1_out, in_1[0]);
  and and_1 (and_1_out, not_1_out, in_2[0]);
  or or_1 (or_1_out, and_1_out, and_2_out);
  not not_2 (not_2_out, in_1[1]);
  and and_2 (and_2_out, not_2_out, in_2[1]);
  or or_2 (or_2_out, or_1_out, or_4_out);
  or or_3 (out_3, or_5_out, or_2_out);
  not not_3 (not_3_out, in_1[2]);
  not not_4 (not_4_out, in_1[3]);
  and and_3 (and_3_out, not_3_out, in_2[2]);
  or or_4 (or_4_out, and_3_out, and_4_out);
  not not_5 (not_5_out, in_1[4]);
  and and_4 (and_4_out, not_4_out, in_2[3]);
  not not_6 (not_6_out, in_1[5]);
  and and_5 (and_5_out, not_5_out, in_2[4]);
  and and_6 (and_6_out, not_6_out, in_2[5]);
  or or_5 (or_5_out, and_5_out, and_6_out);
endmodule
