// Logisim project Exemplo0052.circ as structural Verilog: 3 circuits, main circuit main
module main (
  input  [3:0] a,
  input  [3:0] b,
  input  Carry_In,
  output overFlow,
  output out_5
);

  wire fulladder_2_carryout, fulladder_3_carryout, fulladder_4_carryout, xor_1_out, xor_2_out, xor_3_out,
       xor_4_out;
  wire [3:0] fulladder_4_s;

  // Probe on a
  xor xor_1 (xor_1_out, b[3], Carry_In);
  xor xor_2 (xor_2_out, b[2], Carry_In);
  FullAdder fulladder_1 (
    .carryOut(overFlow), .a(a[3]), .b(xor_1_out), .s(fulladder_4_s[3]), .carry_In(fulladder_2_carryout));
  FullAdder fulladder_2 (
    .carryOut(fulladder_2_carryout), .a(a[2]), .b(xor_2_out), .s(fulladder_4_s[2]),
    .carry_In(fulladder_3_carryout));
  // Probe on fulladder_4_s
  // Probe on b
  xor xor_3 (xor_3_out, b[0], Carry_In);
  xor xor_4 (xor_4_out, b[1], Carry_In);
  FullAdder fulladder_3 (
    .carryOut(fulladder_3_carryout), .a(a[1]), .b(xor_4_out), .s(fulladder_4_s[1]),
    .carry_In(fulladder_4_carryout));
  FullAdder fulladder_4 (
    .carryOut(fulladder_4_carryout), .a(a[0]), .b(xor_3_out), .s(fulladder_4_s[0]), .carry_In(Carry_In));
  nor nor_1 (out_5, fulladder_4_s[3], fulladder_4_s[2], fulladder_4_s[1], fulladder_4_s[0]);
endmodule

// H.A
module HalfAdder (
  input  a,
  input  b,
  output out_3,
  output out_4
);

  and and_1 (out_3, a, b);
  xor xor_1 (out_4, a, b);
endmodule

// F.A.
module FullAdder (
  input  a,
  input  b,
  input  carry_In,
  output carryOut,
  output s
);

  wire halfadder_1_out_3, halfadder_1_out_4, halfadder_2_out_3;

  or or_1 (carryOut, halfadder_1_out_3, halfadder_2_out_3);
  HalfAdder halfadder_1 (.a(a), .b(b), .out_3(halfadder_1_out_3), .out_4(halfadder_1_out_4));
  HalfAdder halfadder_2 (.a(halfadder_1_out_4), .b(carry_In), .out_3(halfadder_2_out_3), .out_4(s));
endmodule
