// Logisim project Exemplo0055.circ as structural Verilog: 3 circuits, main circuit main
module main (
  input  [3:0] in_1,
  input  [3:0] in_2
);

  wire fulladder_1_carryout, fulladder_1_s, fulladder_3_carryout, fulladder_3_s, fulladder_4_carryout,
       fulladder_4_s, fulladder_6_carryout, fulladder_7_carryout, fulladder_7_s, fulladder_8_carryout,
       fulladder_8_s, fulladder_9_carryout, fulladder_10_carryout, fulladder_11_carryout, fulladder_11_s,
       xor_1_out, xor_2_out, xor_3_out, xor_4_out, xor_6_out, xor_7_out, xor_8_out, xor_9_out, xor_10_out,
       xor_11_out, xor_12_out;

  // Probe on in_1
  xor xor_1 (xor_1_out, in_1[3], in_1[2]);
  xor xor_2 (xor_2_out, in_1[3], in_1[3]);
  fullAdder fulladder_1 (
    .carryOut(fulladder_1_carryout), .a(1'b0), .b(xor_1_out), .s(fulladder_1_s),
    .carry_In(fulladder_3_carryout));
  fullAdder fulladder_2 (.a(1'b0), .b(xor_2_out), .carry_In(fulladder_1_carryout));  // open: carryOut, s
  xor xor_3 (xor_3_out, in_1[3], in_1[1]);
  xor xor_4 (xor_4_out, in_1[3], in_1[0]);
  fullAdder fulladder_3 (
    .carryOut(fulladder_3_carryout), .a(1'b0), .b(xor_3_out), .s(fulladder_3_s),
    .carry_In(fulladder_4_carryout));
  fullAdder fulladder_4 (
    .carryOut(fulladder_4_carryout), .a(1'b0), .b(xor_4_out), .s(fulladder_4_s), .carry_In(in_1[3]));
  // XOR_Gate xor_5 has open pins: in0=1'b1, in1=fulladder_6_carryout, out=open
  // Probe on in_2
  xor xor_6 (xor_6_out, in_2[3], in_2[3]);
  fullAdder fulladder_5 (.a(1'b0), .b(xor_6_out), .carry_In(fulladder_7_carryout));  // open: carryOut, s
  xor xor_7 (xor_7_out, 1'b1, fulladder_7_s);
  fullAdder fulladder_6 (
    .carryOut(fulladder_6_carryout), .a(fulladder_1_s), .b(xor_7_out), .carry_In(fulladder_9_carryout));  // open: s
  xor xor_8 (xor_8_out, in_2[3], in_2[2]);
  xor xor_9 (xor_9_out, in_2[3], in_2[1]);
  fullAdder fulladder_7 (
    .carryOut(fulladder_7_carryout), .a(1'b0), .b(xor_8_out), .s(fulladder_7_s),
    .carry_In(fulladder_8_carryout));
  fullAdder fulladder_8 (
    .carryOut(fulladder_8_carryout), .a(1'b0), .b(xor_9_out), .s(fulladder_8_s),
    .carry_In(fulladder_11_carryout));
  xor xor_10 (xor_10_out, 1'b1, fulladder_8_s);
  xor xor_11 (xor_11_out, 1'b1, fulladder_11_s);
  fullAdder fulladder_9 (
    .carryOut(fulladder_9_carryout), .a(fulladder_3_s), .b(xor_10_out), .carry_In(fulladder_10_carryout));  // open: s
  fullAdder fulladder_10 (
    .carryOut(fulladder_10_carryout), .a(fulladder_4_s), .b(xor_11_out), .carry_In(1'b1));  // open: s
  xor xor_12 (xor_12_out, in_2[3], in_2[0]);
  fullAdder fulladder_11 (
    .carryOut(fulladder_11_carryout), .a(1'b0), .b(xor_12_out), .s(fulladder_11_s), .carry_In(in_2[3]));
endmodule

// H.A.
module halfAdder (
  input  a,
  input  b,
  output out_3,
  output out_4
);

  and and_1 (out_3, a, b);
  xor xor_1 (out_4, a, b);
endmodule

// F.A.
module fullAdder (
  input  a,
  input  b,
  input  carry_In,
  output carryOut,
  output s
);

  wire halfadder_1_out_3, halfadder_1_out_4, halfadder_2_out_3;

  or or_1 (carryOut, halfadder_1_out_3, halfadder_2_out_3);
  halfAdder halfadder_1 (.a(a), .b(b), .out_3(halfadder_1_out_3), .out_4(halfadder_1_out_4));
  halfAdder halfadder_2 (.a(halfadder_1_out_4), .b(carry_In), .out_3(halfadder_2_out_3), .out_4(s));
endmodule
