// Logisim project Exemplo0048.circ as structural Verilog
module Resultado_da_operacao (
  input  Carry_In,
  input  [3:0] A,
  input  [3:0] B,
  output Carry_Out,
  output Carry_Out_2,
  output [3:0] out_6
);

  wire [3:0] undriven;

  subtrator_4_bits subtrator_4_bits_1 (.a(undriven), .b(4'b0001), .saida(out_6), .carry_out(Carry_Out_2));
  somador_4_bits somador_4_bits_1 ();
endmodule

// F.A
module Full_Adder (
  input  a,
  input  b,
  input  vem_1,
  output soma,
  output vai_1
);

  wire and_1_out, and_2_out, xor_1_out;

  xor xor_1 (xor_1_out, b, a);
  and and_1 (and_1_out, b, a);
  xor xor_2 (soma, vem_1, xor_1_out);
  and and_2 (and_2_out, vem_1, xor_1_out);
  or or_1 (vai_1, and_2_out, and_1_out);
endmodule

// H.A
module meia_soma (
  input  A,
  input  B,
  output s0,
  output s1
);

  xor xor_1 (s0, A, B);
  and and_1 (s1, A, B);
endmodule

// S.C.4
module subtrator_4_bits (
  input  [3:0] a,
  input  [3:0] b,
  output carry_out,
  output [3:0] saida
);

  wire full_sub_1_vai_1, full_sub_2_vai_1, half_sub_1_s1;

  half_sub half_sub_1 (.A(a[0]), .B(b[0]), .s0(saida[0]), .s1(half_sub_1_s1));
  Full_sub full_sub_1 (.a(a[1]), .b(b[1]), .vem_1(half_sub_1_s1), .soma(saida[1]), .vai_1(full_sub_1_vai_1));
  Full_sub full_sub_2 (.a(a[2]), .b(b[2]), .vem_1(full_sub_1_vai_1), .soma(saida[2]), .vai_1(full_sub_2_vai_1));
  Full_sub full_sub_3 (.a(a[3]), .b(b[3]), .vem_1(full_sub_2_vai_1), .soma(saida[3]), .vai_1(carry_out));
endmodule

// F.S
module Full_sub (
  input  a,
  input  b,
  input  vem_1,
  output soma,
  output vai_1
);

  wire and_1_out, and_2_out, not_1_out, not_2_out, xor_1_out;

  not not_1 (not_1_out, a);
  xor xor_1 (xor_1_out, b, a);
  and and_1 (and_1_out, b, not_1_out);
  not not_2 (not_2_out, xor_1_out);
  xor xor_2 (soma, vem_1, xor_1_out);
  and and_2 (and_2_out, vem_1, not_2_out);
  or or_1 (vai_1, and_2_out, and_1_out);
endmodule

// H.S
module half_sub (
  input  A,
  input  B,
  output s0,
  output s1
);

  wire not_1_out;

  not not_1 (not_1_out, A);
  xor xor_1 (s0, A, B);
  and and_1 (s1, not_1_out, B);
endmodule
