// Logisim project Circuitos.circ as structural Verilog: 7 circuits, main circuit Exemplo0043
module Exemplo0043 (
  input  [3:0] x,
  input  [3:0] y,
  input  Operador,
  output carryOut,
  output [3:0] out_5
);

  wire fulladder_1_carryout, fulladder_2_carryout, fulladder_3_carryout, xor_1_out, xor_2_out, xor_3_out,
       xor_4_out;

  xor xor_1 (xor_1_out, Operador, y[0]);
  fullAdder fulladder_1 (.S0(out_5[0]), .carryOut(fulladder_1_carryout), .x(x[0]), .y(Operador), .carryIn(xor_1_out));
  xor xor_2 (xor_2_out, Operador, y[1]);
  fullAdder fulladder_2 (
    .S0(out_5[1]), .carryOut(fulladder_2_carryout), .x(x[1]), .y(xor_2_out), .carryIn(fulladder_1_carryout));
  xor xor_3 (xor_3_out, Operador, y[2]);
  fullAdder fulladder_3 (
    .S0(out_5[2]), .carryOut(fulladder_3_carryout), .x(x[2]), .y(xor_3_out), .carryIn(fulladder_2_carryout));
  xor xor_4 (xor_4_out, Operador, y[3]);
  fullAdder fulladder_4 (.S0(out_5[3]), .carryOut(carryOut), .x(x[3]), .y(xor_4_out), .carryIn(fulladder_3_carryout));
endmodule

// FA
module fullAdder (
  input  carryIn,
  input  x,
  input  y,
  output S0,
  output carryOut
);

  wire and_1_out, and_2_out, xor_1_out;

  xor xor_1 (xor_1_out, y, x);
  and and_1 (and_1_out, y, x);
  xor xor_2 (S0, carryIn, xor_1_out);
  and and_2 (and_2_out, xor_1_out, carryIn);
  or or_1 (carryOut, and_2_out, and_1_out);
endmodule

module Exemplo0044 (
  input  [3:0] x,
  input  [3:0] y,
  input  Operador,
  output carryOut,
  output out_5,
  output [3:0] out_6
);

  wire fulladder_1_carryout, fulladder_2_carryout, fulladder_3_carryout, xor_1_out, xor_2_out, xor_3_out,
       xor_4_out;

  xor xor_1 (xor_1_out, Operador, y[0]);
  fullAdder fulladder_1 (.S0(out_6[0]), .carryOut(fulladder_1_carryout), .x(x[0]), .y(Operador), .carryIn(xor_1_out));
  xor xor_2 (xor_2_out, Operador, y[1]);
  fullAdder fulladder_2 (
    .S0(out_6[1]), .carryOut(fulladder_2_carryout), .x(x[1]), .y(xor_2_out), .carryIn(fulladder_1_carryout));
  xor xor_3 (xor_3_out, Operador, y[2]);
  fullAdder fulladder_3 (
    .S0(out_6[2]), .carryOut(fulladder_3_carryout), .x(x[2]), .y(xor_3_out), .carryIn(fulladder_2_carryout));
  nor nor_1 (out_5, out_6[0], out_6[1], out_6[2], out_6[3]);
  xor xor_4 (xor_4_out, Operador, y[3]);
  fullAdder fulladder_4 (.S0(out_6[3]), .carryOut(carryOut), .x(x[3]), .y(xor_4_out), .carryIn(fulladder_3_carryout));
endmodule

module Exemplo0045 (
  input  [3:0] in_1,
  output [3:0] out_2,
  output CarryOut
);

  wire halfadder_1_carryout, halfadder_2_carryout, halfadder_3_carryout;

  HalfAdder halfadder_1 (.s0(out_2[0]), .CarryOut(halfadder_1_carryout), .x(in_1[0]), .y(1'b1));
  HalfAdder halfadder_2 (.s0(out_2[1]), .CarryOut(halfadder_2_carryout), .x(halfadder_1_carryout), .y(in_1[1]));
  HalfAdder halfadder_3 (.s0(out_2[2]), .CarryOut(halfadder_3_carryout), .x(halfadder_2_carryout), .y(in_1[2]));
  HalfAdder halfadder_4 (.s0(out_2[3]), .CarryOut(CarryOut), .x(halfadder_3_carryout), .y(in_1[3]));
endmodule

// HA
module HalfAdder (
  input  x,
  input  y,
  output s0,
  output CarryOut
);

  xor xor_1 (s0, y, x);
  and and_1 (CarryOut, y, x);
endmodule

module Exemplo0046 (
  input  [3:0] x,
  output CarryOut,
  output [3:0] out_3
);

  wire fulladder_1_carryout, fulladder_2_carryout, fulladder_3_carryout, halfadder_1_carryout;

  HalfAdder halfadder_1 (.s0(out_3[0]), .CarryOut(halfadder_1_carryout), .x(x[0]), .y(1'b1));
  fullAdder fulladder_1 (
    .S0(out_3[1]), .carryOut(fulladder_1_carryout), .x(x[1]), .y(1'b1), .carryIn(halfadder_1_carryout));
  fullAdder fulladder_2 (
    .S0(out_3[2]), .carryOut(fulladder_2_carryout), .x(x[2]), .y(1'b1), .carryIn(fulladder_1_carryout));
  fullAdder fulladder_3 (
    .S0(out_3[3]), .carryOut(fulladder_3_carryout), .x(x[3]), .y(1'b1), .carryIn(fulladder_2_carryout));
  xor xor_1 (CarryOut, 1'b1, fulladder_3_carryout);
endmodule

module Exemplo0047 (
  input  [3:0] a,
  input  [3:0] b,
  output A___B,
  output A___B_2
);

  wire [2:0] exemplo0043_1_out_5;

  Exemplo0043 exemplo0043_1 (.Operador(1'b1), .x(a), .y(b), .out_5({A___B, exemplo0043_1_out_5}));  // open: carryOut
  not not_1 (A___B_2, A___B);
endmodule
