// Logisim project Exemplo0031.circ as structural Verilog: 4 circuits, main circuit main
module main (
  input  in_1,
  input  a0,
  input  a1,
  input  a2,
  input  a3,
  input  b0,
  input  b1,
  input  b2,
  input  b3,
  output Sinal,
  output Carry_out,
  output s2,
  output s1,
  output s0
);

  wire complemento1_1_out_3, complemento1_2_out_3, complemento1_3_out_3, complemento1_4_out_3,
       fulladder_1_s1, fulladder_2_s1, fulladder_3_s1, fulladder_4_s1;

  complemento1 complemento1_1 (.in_1(b0), .in_2(in_1), .out_3(complemento1_1_out_3));
  complemento1 complemento1_2 (.in_1(b1), .in_2(in_1), .out_3(complemento1_2_out_3));
  complemento1 complemento1_3 (.in_1(b2), .in_2(in_1), .out_3(complemento1_3_out_3));
  complemento1 complemento1_4 (.in_1(b3), .in_2(in_1), .out_3(complemento1_4_out_3));
  fulladder fulladder_1 (.y(a0), .x(complemento1_1_out_3), .c(in_1), .s1(fulladder_1_s1), .s0(s0));
  fulladder fulladder_2 (.y(a1), .x(complemento1_2_out_3), .c(fulladder_1_s1), .s1(fulladder_2_s1), .s0(s1));
  fulladder fulladder_3 (.y(a2), .x(complemento1_3_out_3), .c(fulladder_2_s1), .s1(fulladder_3_s1), .s0(s2));
  fulladder fulladder_4 (.y(a3), .x(complemento1_4_out_3), .c(fulladder_3_s1), .s1(fulladder_4_s1), .s0(Carry_out));
  complemento1 complemento1_5 (.in_1(fulladder_4_s1), .in_2(in_1), .out_3(Sinal));
endmodule

module adder (
  input  x,
  input  y,
  output s0,
  output s1
);

  xor XOR1 (s0, x, y);
  and AND1 (s1, y, x);
endmodule

// FA
module fulladder (
  input  y,
  input  c,
  input  x,
  output s0,
  output s1
);

  wire adder_1_s0, adder_1_s1, adder_2_s1;

  adder adder_1 (.x(y), .y(x), .s0(adder_1_s0), .s1(adder_1_s1));
  adder adder_2 (.x(adder_1_s0), .y(c), .s0(s0), .s1(adder_2_s1));
  or OR1 (s1, adder_2_s1, adder_1_s1);
endmodule

// c1
module complemento1 (
  input  in_1,
  input  in_2,
  output out_3
);

  xor xor_1 (out_3, in_1, in_2);
endmodule
