// Logisim project Exemplo0032.circ as structural Verilog: 5 circuits, main circuit main
module main (
  input  Carry_in,
  input  Amplitude,
  input  Sinal,
  input  in_4,
  input  in_5,
  input  in_6,
  input  in_7,
  input  in_8,
  input  in_9,
  output [1:0] Sinal_2,
  output [2:0] Carry_out,
  output out_12
);

  wire c1_1_s1, c1_2_s1, c1_3_s1, c1_4_s1, fulladder_1_carry_out, fulladder_2_carry_out,
       fulladder_3_carry_out, fulladder_4_carry_out;

  C1 c1_1 (.a(in_6), .b(Carry_in), .s1(c1_1_s1));
  C1 c1_2 (.a(in_9), .b(Carry_in), .s1(c1_2_s1));
  C1 c1_3 (.a(in_8), .b(Carry_in), .s1(c1_3_s1));
  C1 c1_4 (.a(in_7), .b(Carry_in), .s1(c1_4_s1));
  fullAdder fulladder_1 (
    .x(Amplitude), .y(c1_1_s1), .Carry_in(Carry_in), .Carry_out(fulladder_1_carry_out), .s2(Carry_out[0]));
  fullAdder fulladder_2 (
    .x(in_5), .y(c1_2_s1), .Carry_in(fulladder_1_carry_out), .Carry_out(fulladder_2_carry_out),
    .s2(Carry_out[1]));
  fullAdder fulladder_3 (
    .x(in_4), .y(c1_3_s1), .Carry_in(fulladder_2_carry_out), .Carry_out(fulladder_3_carry_out),
    .s2(Carry_out[2]));
  fullAdder fulladder_4 (
    .x(Sinal), .y(c1_4_s1), .Carry_in(fulladder_3_carry_out), .Carry_out(fulladder_4_carry_out),
    .s2(Sinal_2[0]));
  C1 c1_5 (.a(fulladder_4_carry_out), .b(Carry_in), .s1(Sinal_2[1]));
  _1OR0 u_1or0_1 (.in_1(Carry_out[0]), .in_2(Carry_out[1]), .in_3(Carry_out[2]), .out_4(out_12));

  // Notes on the sheet:
  //   0 - SOMAR
  //   1-SUBITRAIR
  //   Amplitude
endmodule

// F.Adder
module fullAdder (
  input  x,
  input  y,
  input  Carry_in,
  output s2,
  output Carry_out
);

  wire adder_1_s0, adder_1_s1, adder_2_s1;

  Adder adder_1 (.a(y), .b(x), .s0(adder_1_s0), .s1(adder_1_s1));
  Adder adder_2 (.a(adder_1_s0), .b(Carry_in), .s0(s2), .s1(adder_2_s1));
  or OR1 (Carry_out, adder_2_s1, adder_1_s1);
endmodule

module Adder (
  input  a,
  input  b,
  output s0,
  output s1
);

  xor XOR1 (s0, a, b);
  and AND1 (s1, b, a);
endmodule

// c1
module C1 (
  input  a,
  input  b,
  output s1
);

  xor XOR1 (s1, a, b);
endmodule

// 1or0
module _1OR0 (
  input  in_1,
  input  in_2,
  input  in_3,
  output out_4
);

  nor nor_1 (out_4, in_1, in_2, in_3);
endmodule
