// Logisim project Exemplo0034.circ as structural Verilog: 5 circuits, main circuit main
module main (
  input  Carry_in,
  input  Amplitude,
  input  Sinal,
  input  in_4,
  input  in_5,
  input  in_6,
  input  in_7,
  input  in_8,
  input  in_9,
  output [2:0] Amplitude_2,
  output Sinal_2,
  output Carry_out
);

  wire c1_1_s1, c1_2_s1, c1_3_s1, c1_4_s1, fulladder_1_carry_out, fulladder_1_s2, fulladder_2_carry_out,
       fulladder_2_s2, fulladder_3_carry_out, fulladder_3_s2, fulladder_4_carry_out, fulladder_4_s2;

  C1 c1_1 (.a(in_6), .b(Carry_in), .s1(c1_1_s1));
  C1 c1_2 (.a(in_9), .b(Carry_in), .s1(c1_2_s1));
  C1 c1_3 (.a(in_8), .b(Carry_in), .s1(c1_3_s1));
  C1 c1_4 (.a(in_7), .b(Carry_in), .s1(c1_4_s1));
  fullAdder fulladder_1 (
    .x(Amplitude), .y(c1_1_s1), .Carry_in(Carry_in), .Carry_out(fulladder_1_carry_out), .s2(fulladder_1_s2));
  fullAdder fulladder_2 (
    .x(in_5), .y(c1_2_s1), .Carry_in(fulladder_1_carry_out), .Carry_out(fulladder_2_carry_out),
    .s2(fulladder_2_s2));
  fullAdder fulladder_3 (
    .x(in_4), .y(c1_3_s1), .Carry_in(fulladder_2_carry_out), .Carry_out(fulladder_3_carry_out),
    .s2(fulladder_3_s2));
  fullAdder fulladder_4 (
    .x(Sinal), .y(c1_4_s1), .Carry_in(fulladder_3_carry_out), .Carry_out(fulladder_4_carry_out),
    .s2(fulladder_4_s2));
  C1 c1_5 (.a(fulladder_4_carry_out), .b(Carry_in), .s1(Sinal_2));
  Decremeno1 decremeno1_1 (
    .x(fulladder_1_s2), .y(fulladder_2_s2), .z(fulladder_3_s2), .carryout(Carry_out), .s2(Amplitude_2[2]),
    .s1(Amplitude_2[1]), .s0(Amplitude_2[0]), .carryin(fulladder_4_s2));

  // Notes on the sheet:
  //   0 - SOMAR
  //   1-SUBITRAIR
  //   Tive problemas no Carry_out apos o decremento de 1
endmodule

module Adder (
  input  a,
  input  b,
  output s0,
  output s1
);

  xor XOR1 (s0, a, b);
  and AND1 (s1, b, a);
endmodule

module fullAdder (
  input  x,
  input  y,
  input  Carry_in,
  output s2,
  output Carry_out
);

  wire adder_1_s0, adder_1_s1, adder_2_s1;

  Adder adder_1 (.a(y), .b(x), .s0(adder_1_s0), .s1(adder_1_s1));
  Adder adder_2 (.a(adder_1_s0), .b(Carry_in), .s0(s2), .s1(adder_2_s1));
  or OR1 (Carry_out, adder_2_s1, adder_1_s1);
endmodule

module C1 (
  input  a,
  input  b,
  output s1
);

  xor XOR1 (s1, a, b);
endmodule

// Dercrement
module Decremeno1 (
  input  x,
  input  y,
  input  z,
  input  carryin,
  output carryout,
  output s2,
  output s1,
  output s0
);

  wire fulladder_1_carry_out, fulladder_2_carry_out;

  fullAdder fulladder_1 (.x(x), .y(1'b1), .Carry_in(carryin), .Carry_out(fulladder_1_carry_out), .s2(s0));
  fullAdder fulladder_2 (.x(y), .y(1'b1), .Carry_in(fulladder_1_carry_out), .Carry_out(fulladder_2_carry_out), .s2(s1));
  fullAdder fulladder_3 (.x(z), .y(1'b1), .Carry_in(fulladder_2_carry_out), .Carry_out(carryout), .s2(s2));
endmodule
