// Logisim project Exemplo0035.circ as structural Verilog: 2 circuits, main circuit main
module main (
  input  in_1,
  input  in_2,
  input  in_3,
  input  in_4,
  input  in_5,
  input  in_6,
  input  in_7,
  input  in_8,
  output out_9
);

  wire a_b_1_out_5, a_b_2_out_5;

  A___B a_b_1 (.in_1(in_2), .in_2(in_3), .in_3(in_7), .in_4(in_5), .out_5(a_b_1_out_5));
  A___B a_b_2 (.in_1(in_4), .in_2(in_1), .in_3(in_8), .in_4(in_6), .out_5(a_b_2_out_5));
  or or_1 (out_9, a_b_1_out_5, a_b_2_out_5);

  // Notes on the sheet:
  //   Nao consegui fazer a comparaçao para o quarto bit for o sinal
endmodule

module A___B (
  input  in_1,
  input  in_2,
  input  in_3,
  input  in_4,
  output out_5
);

  wire and_1_out, and_2_out, and_3_out, not_1_out, not_2_out, xnor_1_out;

  not not_1 (not_1_out, in_4);
  not not_2 (not_2_out, in_3);
  xnor xnor_1 (xnor_1_out, in_3, in_1);
  and and_1 (and_1_out, in_2, not_1_out);
  and and_2 (and_2_out, not_2_out, in_1);
  and and_3 (and_3_out, xnor_1_out, and_1_out);
  or or_1 (out_5, and_3_out, and_2_out);
endmodule
