// Logisim project Exemplo0032.circ as structural Verilog: 5 circuits, main circuit HalfAdder
// HA
module HalfAdder (
  input  in_1,
  input  in_2,
  output out_3,
  output out_4
);

  xor xor_1 (out_3, in_1, in_2);
  and and_1 (out_4, in_2, in_1);
endmodule

// FU
module FullAdder (
  input  in_1,
  input  in_2,
  input  in_3,
  output out_4,
  output out_5
);

  wire halfadder_1_out_3, halfadder_1_out_4, halfadder_2_out_4;

  HalfAdder halfadder_1 (.in_1(in_2), .in_2(in_3), .out_3(halfadder_1_out_3), .out_4(halfadder_1_out_4));
  HalfAdder halfadder_2 (.in_1(halfadder_1_out_3), .in_2(in_1), .out_3(out_4), .out_4(halfadder_2_out_4));
  or or_1 (out_5, halfadder_1_out_4, halfadder_2_out_4);
endmodule

// FU2
module FullAdder2 (
  input  Carry_In,
  input  a0,
  input  a1,
  input  a2,
  input  Sinal_a,
  input  b0,
  input  b1,
  input  b2,
  input  Sinal_b,
  output out_10,
  output out_11,
  output out_12,
  output out_13,
  output out_14,
  output out_15
);

  wire complemento1_1_s1, complemento1_2_s1, complemento1_3_s1, complemento1_4_s1, fulladder_1_out_5,
       fulladder_2_out_5, fulladder_3_out_5, fulladder_4_out_5;

  Complemento1 complemento1_1 (.a(b0), .b(Carry_In), .s1(complemento1_1_s1));
  Complemento1 complemento1_2 (.a(b1), .b(Carry_In), .s1(complemento1_2_s1));
  Complemento1 complemento1_3 (.a(b2), .b(Carry_In), .s1(complemento1_3_s1));
  Complemento1 complemento1_4 (.a(Sinal_b), .b(Carry_In), .s1(complemento1_4_s1));
  FullAdder fulladder_1 (
    .in_2(a0), .in_3(complemento1_1_s1), .in_1(Carry_In), .out_5(fulladder_1_out_5), .out_4(out_14));
  FullAdder fulladder_2 (
    .in_2(a1), .in_3(complemento1_2_s1), .in_1(fulladder_1_out_5), .out_5(fulladder_2_out_5), .out_4(out_13));
  FullAdder fulladder_3 (
    .in_2(a2), .in_3(complemento1_3_s1), .in_1(fulladder_2_out_5), .out_5(fulladder_3_out_5), .out_4(out_12));
  FullAdder fulladder_4 (
    .in_2(Sinal_a), .in_3(complemento1_4_s1), .in_1(fulladder_3_out_5), .out_5(fulladder_4_out_5),
    .out_4(out_11));
  Complemento1 complemento1_5 (.a(fulladder_4_out_5), .b(Carry_In), .s1(out_10));
  Zero zero_1 (.in_1(out_14), .in_2(out_13), .in_3(out_12), .in_4(out_11), .out_5(out_15));

  // Notes on the sheet:
  //   1 - Zero 
  //   0 - Diferente de zero
endmodule

// C1
module Complemento1 (
  input  a,
  input  b,
  output s1
);

  xor XOR (s1, a, b);
endmodule

// ZERO
module Zero (
  input  in_1,
  input  in_2,
  input  in_3,
  input  in_4,
  output out_5
);

  nor nor_1 (out_5, in_1, in_2, in_3, in_4);

  // Notes on the sheet:
  //   Se a operacao é igual a zero = 1
  //   Diferente de zero = 0;
endmodule
