// Logisim project Exemplo0033.circ as structural Verilog: 4 circuits, main circuit HalfAdder
// HA
module HalfAdder (
  input  in_1,
  input  in_2,
  output out_3,
  output out_4
);

  xor xor_1 (out_3, in_1, in_2);
  and and_1 (out_4, in_2, in_1);
endmodule

// FU
module FullAdder (
  input  in_1,
  input  in_2,
  input  in_3,
  output out_4,
  output out_5
);

  wire halfadder_1_out_3, halfadder_1_out_4, halfadder_2_out_4;

  HalfAdder halfadder_1 (.in_1(in_2), .in_2(in_3), .out_3(halfadder_1_out_3), .out_4(halfadder_1_out_4));
  HalfAdder halfadder_2 (.in_1(halfadder_1_out_3), .in_2(in_1), .out_3(out_4), .out_4(halfadder_2_out_4));
  or or_1 (out_5, halfadder_1_out_4, halfadder_2_out_4);
endmodule

module FullAdder2 (
  input  Carry_In,
  input  a0,
  input  a1,
  input  a2,
  input  Sinal_a,
  input  b0,
  input  b1,
  input  b2,
  input  Sinal_b,
  output out_10,
  output out_11,
  output out_12,
  output out_13,
  output out_14
);

  wire fulladder_1_out_4, fulladder_1_out_5, fulladder_2_out_4, fulladder_2_out_5, fulladder_3_out_4,
       fulladder_3_out_5, fulladder_4_out_5;

  FullAdder fulladder_1 (.in_2(a0), .in_3(b0), .in_1(Carry_In), .out_5(fulladder_1_out_5), .out_4(fulladder_1_out_4));
  FullAdder fulladder_2 (
    .in_2(a1), .in_3(b1), .in_1(fulladder_1_out_5), .out_5(fulladder_2_out_5), .out_4(fulladder_2_out_4));
  FullAdder fulladder_3 (
    .in_2(a2), .in_3(b2), .in_1(fulladder_2_out_5), .out_5(fulladder_3_out_5), .out_4(fulladder_3_out_4));
  FullAdder fulladder_4 (
    .in_2(Sinal_a), .in_3(Sinal_b), .in_1(fulladder_3_out_5), .out_5(fulladder_4_out_5), .out_4(out_10));
  Incremento1 incremento1_1 (
    .in_1(fulladder_1_out_4), .in_2(fulladder_2_out_4), .in_3(fulladder_3_out_4), .out_5(out_11),
    .out_6(out_12), .out_7(out_13), .out_8(out_14), .in_4(fulladder_4_out_5));
endmodule

// INC1
module Incremento1 (
  input  in_1,
  input  in_2,
  input  in_3,
  input  in_4,
  output out_5,
  output out_6,
  output out_7,
  output out_8
);

  wire fulladder_1_out_5, fulladder_2_out_5;

  FullAdder fulladder_1 (.in_2(in_1), .in_3(1'b1), .in_1(in_4), .out_5(fulladder_1_out_5), .out_4(out_8));
  FullAdder fulladder_2 (.in_2(in_2), .in_3(1'b0), .in_1(fulladder_1_out_5), .out_5(fulladder_2_out_5), .out_4(out_7));
  FullAdder fulladder_3 (.in_2(in_3), .in_3(1'b0), .in_1(fulladder_2_out_5), .out_5(out_5), .out_4(out_6));
endmodule
