// Logisim project Exemplo0032_logisim.circ as structural Verilog: 5 circuits, main circuit main
module main (
  input  a3,
  input  a2,
  input  a1,
  input  a0,
  input  carryIn,
  input  b3,
  input  b2,
  input  b1,
  input  b0,
  output s3,
  output s2,
  output s1,
  output s0,
  output e_igual_a_zero
);

  SomadorSubtrator somadorsubtrator_1 (
    .a3(a3), .a2(a2), .a1(a1), .a0(a0), .carryIn(carryIn), .b3(b3), .b2(b2), .b1(b1), .b0(b0), .s0(s0),
    .s1(s1), .s2(s2), .s3(s3));
  determinarZero determinarzero_1 (.a3(s3), .a2(s2), .a1(s1), .a0(s0), .s(e_igual_a_zero));
endmodule

module SomadorSubtrator (
  input  a3,
  input  a2,
  input  a1,
  input  a0,
  input  carryIn,
  input  b3,
  input  b2,
  input  b1,
  input  b0,
  output s0,
  output s1,
  output s2,
  output s3
);

  wire fulladder_1_s1, fulladder_2_s1, fulladder_3_s1, xor_1_out, xor_2_out, xor_3_out, xor_4_out;

  xor xor_1 (xor_1_out, carryIn, b0);
  fullAdder fulladder_1 (.a(a0), .b(xor_1_out), .c(carryIn), .s0(s0), .s1(fulladder_1_s1));
  xor xor_2 (xor_2_out, carryIn, b1);
  xor xor_3 (xor_3_out, carryIn, b2);
  xor xor_4 (xor_4_out, carryIn, b3);
  fullAdder fulladder_2 (.a(a1), .b(xor_2_out), .c(fulladder_1_s1), .s0(s1), .s1(fulladder_2_s1));
  fullAdder fulladder_3 (.a(a2), .b(xor_3_out), .c(fulladder_2_s1), .s0(s2), .s1(fulladder_3_s1));
  fullAdder fulladder_4 (.a(a3), .b(xor_4_out), .c(fulladder_3_s1), .s0(s3));  // open: s1
endmodule

module fullAdder (
  input  a,
  input  b,
  input  c,
  output s0,
  output s1
);

  wire halfadder_1_c, halfadder_1_s, halfadder_2_c;

  halfAdder halfadder_1 (.a(a), .b(b), .s(halfadder_1_s), .c(halfadder_1_c));
  halfAdder halfadder_2 (.a(halfadder_1_s), .b(c), .s(s0), .c(halfadder_2_c));
  or or_1 (s1, halfadder_2_c, halfadder_1_c);
endmodule

module halfAdder (
  input  a,
  input  b,
  output s,
  output c
);

  xor xor_1 (s, a, b);
  and and_1 (c, a, b);
endmodule

module determinarZero (
  input  a3,
  input  a2,
  input  a1,
  input  a0,
  output s
);

  nor nor_1 (s, a0, a1, a2, a3);
endmodule
