// Logisim project Exemplo0035_logisim.circ as structural Verilog: 10 circuits, main circuit main
module main (
  input  a3,
  input  a2,
  input  a1,
  input  a0,
  input  um,
  input  b3,
  input  b2,
  input  b1,
  input  b0,
  output menor,
  output maior,
  output igual
);

  comparar comparar_1 (
    .a3(a3), .a2(a2), .a1(a1), .a0(a0), .um(um), .b3(b3), .b2(b2), .b1(b1), .b0(b0), .menor(menor),
    .maior(maior), .igual(igual));  // open: s0, s1, s2, s3, s4

  // Notes on the sheet:
  //   Não sei como usar uma constante, mas a entrada com rótulo "um" deve ser sempre igual a 1.
endmodule

module SomadorSubtrator (
  input  a3,
  input  a2,
  input  a1,
  input  a0,
  input  carryIn,
  input  b3,
  input  b2,
  input  b1,
  input  b0,
  output s0,
  output s1,
  output s2,
  output s3
);

  wire fulladder_1_s1, fulladder_2_s1, fulladder_3_s1, xor_1_out, xor_2_out, xor_3_out, xor_4_out;

  xor xor_1 (xor_1_out, carryIn, b0);
  fullAdder fulladder_1 (.a(a0), .b(xor_1_out), .c(carryIn), .s0(s0), .s1(fulladder_1_s1));
  xor xor_2 (xor_2_out, carryIn, b1);
  xor xor_3 (xor_3_out, carryIn, b2);
  xor xor_4 (xor_4_out, carryIn, b3);
  fullAdder fulladder_2 (.a(a1), .b(xor_2_out), .c(fulladder_1_s1), .s0(s1), .s1(fulladder_2_s1));
  fullAdder fulladder_3 (.a(a2), .b(xor_3_out), .c(fulladder_2_s1), .s0(s2), .s1(fulladder_3_s1));
  fullAdder fulladder_4 (.a(a3), .b(xor_4_out), .c(fulladder_3_s1), .s0(s3));  // open: s1
endmodule

module fullAdder (
  input  a,
  input  b,
  input  c,
  output s0,
  output s1
);

  wire halfadder_1_c, halfadder_1_s, halfadder_2_c;

  halfAdder halfadder_1 (.a(a), .b(b), .s(halfadder_1_s), .c(halfadder_1_c));
  halfAdder halfadder_2 (.a(halfadder_1_s), .b(c), .s(s0), .c(halfadder_2_c));
  or or_1 (s1, halfadder_2_c, halfadder_1_c);
endmodule

module halfAdder (
  input  a,
  input  b,
  output s,
  output c
);

  xor xor_1 (s, a, b);
  and and_1 (c, a, b);
endmodule

module determinarZero (
  input  a3,
  input  a2,
  input  a1,
  input  a0,
  output s
);

  nor nor_1 (s, a0, a1, a2, a3);
endmodule

module incrementar (
  input  a3,
  input  a2,
  input  a1,
  input  a0,
  input  zero,
  input  zero3,
  input  zero2,
  input  zero1,
  output s0,
  output s1,
  output s2,
  output s3
);

  wire not_1_out;

  SomadorSubtrator somadorsubtrator_1 (
    .a3(a3), .a2(a2), .a1(a1), .a0(a0), .carryIn(zero), .b3(zero3), .b2(zero2), .b1(zero1), .b0(not_1_out),
    .s0(s0), .s1(s1), .s2(s2), .s3(s3));
  not not_1 (not_1_out, zero);

  // Notes on the sheet:
  //   As entradas de rótulos "zero3", "zero2" e "zero1" devem ser iguais a 0.
  //   Não sei como usar uma constante, mas a entrada com rótulo "zero" deve ser sempre igual a 0.
endmodule

module decrementar (
  input  a3,
  input  a2,
  input  a1,
  input  a0,
  input  um,
  input  zero3,
  input  zero2,
  input  zero1,
  output s0,
  output s1,
  output s2,
  output s3
);

  SomadorSubtrator somadorsubtrator_1 (
    .a3(a3), .a2(a2), .a1(a1), .a0(a0), .carryIn(um), .b3(zero3), .b2(zero2), .b1(zero1), .b0(um), .s0(s0),
    .s1(s1), .s2(s2), .s3(s3));

  // Notes on the sheet:
  //   As entradas de rótulos "zero3", "zero2" e "zero1" devem ser iguais a 0.
  //   Não sei como usar uma constante, mas a entrada com rótulo "um" deve ser sempre igual a 1.
endmodule

module comparar (
  input  a3,
  input  a2,
  input  a1,
  input  a0,
  input  um,
  input  b2,
  input  b1,
  input  b0,
  input  b3,
  output s0,
  output s1,
  output s2,
  output s3,
  output s4,
  output menor,
  output maior,
  output igual
);

  wire not_1_out, not_2_out, or_1_out, xnor_1_out;

  SomadorSubtrator5bits somadorsubtrator5bits_1 (
    .a3(a3), .a2(a2), .a1(a1), .a0(a0), .carryIn(um), .b3(b3), .b2(b2), .b1(b1), .b0(b0), .s0(s0), .s1(s1),
    .s2(s2), .s3(s3), .s4(s4));
  or or_1 (or_1_out, s3, s2, s1, s0);
  not not_1 (not_1_out, s4);
  multiplexador multiplexador_1 (.a(s4), .b(not_1_out), .chave(xnor_1_out), .s(menor));
  xnor xnor_1 (xnor_1_out, a3, b3);
  not not_2 (not_2_out, menor);
  and and_1 (maior, not_2_out, or_1_out);
  xnor xnor_2 (igual, menor, maior);

  // Notes on the sheet:
  //   Não sei como usar uma constante, mas a entrada com rótulo "um" deve ser sempre igual a 1.
endmodule

module SomadorSubtrator5bits (
  input  a3,
  input  a2,
  input  a1,
  input  a0,
  input  carryIn,
  input  b3,
  input  b2,
  input  b1,
  input  b0,
  output s0,
  output s1,
  output s2,
  output s3,
  output s4
);

  wire fulladder_1_s1, fulladder_2_s1, fulladder_3_s1, xor_1_out, xor_2_out, xor_3_out, xor_4_out;

  xor xor_1 (xor_1_out, carryIn, b0);
  fullAdder fulladder_1 (.a(a0), .b(xor_1_out), .c(carryIn), .s0(s0), .s1(fulladder_1_s1));
  xor xor_2 (xor_2_out, carryIn, b1);
  xor xor_3 (xor_3_out, carryIn, b2);
  xor xor_4 (xor_4_out, carryIn, b3);
  fullAdder fulladder_2 (.a(a1), .b(xor_2_out), .c(fulladder_1_s1), .s0(s1), .s1(fulladder_2_s1));
  fullAdder fulladder_3 (.a(a2), .b(xor_3_out), .c(fulladder_2_s1), .s0(s2), .s1(fulladder_3_s1));
  fullAdder fulladder_4 (.a(a3), .b(xor_4_out), .c(fulladder_3_s1), .s0(s3), .s1(s4));
endmodule

module multiplexador (
  input  a,
  input  b,
  input  chave,
  output s
);

  wire and_1_out, and_2_out, not_1_out;

  and and_1 (and_1_out, b, chave);
  not not_1 (not_1_out, chave);
  and and_2 (and_2_out, not_1_out, a);
  or or_1 (s, and_1_out, and_2_out);
endmodule
