// Logisim project Exemplo0035.circ as structural Verilog: 7 circuits, main circuit A>B
module A_B (
  input  in_1,
  input  in_2,
  output out_3
);

  wire not_1_out;

  and and_1 (out_3, in_1, not_1_out);
  not not_1 (not_1_out, in_2);
endmodule

module main (
  input  a0,
  input  a1,
  input  a2,
  input  a3,
  input  b0,
  input  b1,
  input  b2,
  input  b3,
  output out_9,
  output out_10,
  output out_11
);

  A_B_4bits a_b_4bits_1 (
    .in_1(a0), .in_2(a1), .in_3(a2), .in_4(a3), .in_5(b0), .in_6(b1), .in_7(b2), .in_8(b3), .out_9(out_9));
  B_A_4bits b_a_4bits_1 (
    .in_1(a0), .in_2(a1), .in_3(a2), .in_4(a3), .in_5(b0), .in_6(b1), .in_7(b2), .in_8(b3), .out_9(out_10));
  igualador_4bits igualador_4bits_1 (
    .in_1(a0), .in_2(a1), .in_3(a2), .in_4(a3), .in_5(b0), .in_6(b1), .in_7(b2), .in_8(b3), .out_9(out_11));
endmodule

// A>B
module A_B_4bits (
  input  in_1,
  input  in_2,
  input  in_3,
  input  in_4,
  input  in_5,
  input  in_6,
  input  in_7,
  input  in_8,
  output out_9
);

  wire a_b_1_out_3, a_b_2_out_3, a_b_3_out_3, a_b_4_out_3;

  A_B a_b_1 (.in_1(in_1), .in_2(in_5), .out_3(a_b_1_out_3));
  A_B a_b_2 (.in_1(in_2), .in_2(in_6), .out_3(a_b_2_out_3));
  A_B a_b_3 (.in_1(in_3), .in_2(in_7), .out_3(a_b_3_out_3));
  A_B a_b_4 (.in_1(in_4), .in_2(in_8), .out_3(a_b_4_out_3));
  or or_1 (out_9, a_b_1_out_3, a_b_2_out_3, a_b_3_out_3, a_b_4_out_3);
endmodule

module igualador (
  input  in_1,
  input  in_2,
  output out_3
);

  xnor xnor_1 (out_3, in_1, in_2);
endmodule

module B_A (
  input  in_1,
  input  in_2,
  output out_3
);

  wire not_1_out;

  not not_1 (not_1_out, in_1);
  and and_1 (out_3, not_1_out, in_2);
endmodule

// B>A
module B_A_4bits (
  input  in_1,
  input  in_2,
  input  in_3,
  input  in_4,
  input  in_5,
  input  in_6,
  input  in_7,
  input  in_8,
  output out_9
);

  wire b_a_1_out_3, b_a_2_out_3, b_a_3_out_3, b_a_4_out_3;

  B_A b_a_1 (.in_1(in_1), .in_2(in_5), .out_3(b_a_1_out_3));
  B_A b_a_2 (.in_1(in_2), .in_2(in_6), .out_3(b_a_2_out_3));
  B_A b_a_3 (.in_1(in_3), .in_2(in_7), .out_3(b_a_3_out_3));
  B_A b_a_4 (.in_1(in_4), .in_2(in_8), .out_3(b_a_4_out_3));
  or or_1 (out_9, b_a_1_out_3, b_a_2_out_3, b_a_3_out_3, b_a_4_out_3);
endmodule

// IGUAL
module igualador_4bits (
  input  in_1,
  input  in_2,
  input  in_3,
  input  in_4,
  input  in_5,
  input  in_6,
  input  in_7,
  input  in_8,
  output out_9
);

  wire igualador_1_out_3, igualador_2_out_3, igualador_3_out_3, igualador_4_out_3;

  igualador igualador_1 (.in_1(in_1), .in_2(in_5), .out_3(igualador_1_out_3));
  igualador igualador_2 (.in_1(in_2), .in_2(in_6), .out_3(igualador_2_out_3));
  igualador igualador_3 (.in_1(in_3), .in_2(in_7), .out_3(igualador_3_out_3));
  igualador igualador_4 (.in_1(in_4), .in_2(in_8), .out_3(igualador_4_out_3));
  and and_1 (out_9, igualador_1_out_3, igualador_2_out_3, igualador_3_out_3, igualador_4_out_3);
endmodule
