// Logisim project Exemplo0045.circ as structural Verilog: 3 circuits, main circuit meia-soma
// S.C 4
module somador_4_bits (
  input  Carry_In,
  input  [3:0] A,
  input  [3:0] B,
  output out_4,
  output [3:0] out_5
);

  wire full_adder_1_vai_1, full_adder_2_vai_1, full_adder_3_vai_1, xor_1_out, xor_2_out, xor_3_out, xor_4_out;

  Full_Adder full_adder_1 (.a(A[0]), .b(xor_1_out), .vem_1(Carry_In), .soma(out_5[0]), .vai_1(full_adder_1_vai_1));
  xor xor_1 (xor_1_out, B[0], Carry_In);
  Full_Adder full_adder_2 (
    .a(A[1]), .b(xor_2_out), .vem_1(full_adder_1_vai_1), .soma(out_5[1]), .vai_1(full_adder_2_vai_1));
  xor xor_2 (xor_2_out, B[1], Carry_In);
  xor xor_3 (xor_3_out, Carry_In, B[2]);
  Full_Adder full_adder_3 (
    .a(A[2]), .b(xor_3_out), .vem_1(full_adder_2_vai_1), .soma(out_5[2]), .vai_1(full_adder_3_vai_1));
  xor xor_4 (xor_4_out, Carry_In, B[3]);
  Full_Adder full_adder_4 (.a(A[3]), .b(xor_4_out), .vem_1(full_adder_3_vai_1), .soma(out_5[3]), .vai_1(out_4));
endmodule

// F.A
module Full_Adder (
  input  a,
  input  b,
  input  vem_1,
  output soma,
  output vai_1
);

  wire and_1_out, and_2_out, xor_1_out;

  xor xor_1 (xor_1_out, b, a);
  and and_1 (and_1_out, b, a);
  xor xor_2 (soma, vem_1, xor_1_out);
  and and_2 (and_2_out, vem_1, xor_1_out);
  or or_1 (vai_1, and_2_out, and_1_out);
endmodule

// H.A
module meia_soma (
  input  A,
  input  B,
  output s0,
  output s1
);

  xor xor_1 (s0, A, B);
  and and_1 (s1, A, B);
endmodule
