// Logisim project Exemplo0049.circ as structural Verilog: 4 circuits, main circuit meia-sub
module Resultado_da_operacao (
  input  [3:0] a,
  input  [3:0] b,
  output carry_out
);

  subtrator_4_bits subtrator_4_bits_1 (.A(a), .B(b), .carry_out(carry_out));  // open: saida
endmodule

// S.C 2
module subtrator_4_bits (
  input  [3:0] A,
  input  [3:0] B,
  output carry_out,
  output [3:0] saida
);

  wire full_sub_1_vai_1, full_sub_2_vai_1, meia_sub_1_s1;

  meia_sub meia_sub_1 (.A(A[0]), .B(B[0]), .s0(saida[0]), .s1(meia_sub_1_s1));
  Full_sub full_sub_1 (.a(A[1]), .b(B[1]), .vem_1(meia_sub_1_s1), .soma(saida[1]), .vai_1(full_sub_1_vai_1));
  Full_sub full_sub_2 (.a(A[2]), .b(B[2]), .vem_1(full_sub_1_vai_1), .soma(saida[2]), .vai_1(full_sub_2_vai_1));
  Full_sub full_sub_3 (.a(A[3]), .b(B[3]), .vem_1(full_sub_2_vai_1), .soma(carry_out), .vai_1(saida[3]));
endmodule

// F.S
module Full_sub (
  input  a,
  input  b,
  input  vem_1,
  output soma,
  output vai_1
);

  wire and_1_out, and_2_out, not_1_out, not_2_out, xor_1_out;

  not not_1 (not_1_out, a);
  xor xor_1 (xor_1_out, b, a);
  and and_1 (and_1_out, b, not_1_out);
  not not_2 (not_2_out, xor_1_out);
  xor xor_2 (soma, vem_1, xor_1_out);
  and and_2 (and_2_out, vem_1, not_2_out);
  or or_1 (vai_1, and_2_out, and_1_out);
endmodule

// H.S
module meia_sub (
  input  A,
  input  B,
  output s0,
  output s1
);

  wire not_1_out;

  not not_1 (not_1_out, A);
  xor xor_1 (s0, A, B);
  and and_1 (s1, not_1_out, B);
endmodule
