// Logisim project Ex 31 - 32.circ as structural Verilog
// FA
module FullAdder (
  input  ci,
  input  in_2,
  input  in_3,
  output s0,
  output co
);

  wire and_1_out, and_2_out, xor_1_out;

  xor xor_1 (xor_1_out, in_3, in_2);
  and and_1 (and_1_out, in_3, in_2);
  xor xor_2 (s0, ci, xor_1_out);
  and and_2 (and_2_out, xor_1_out, ci);
  or or_1 (co, and_2_out, and_1_out);
endmodule

// +/-
module Exemplo0031 (
  input  [3:0] a,
  input  [3:0] b,
  input  op,
  output bit_Overflow,
  output [3:0] out_5
);

  wire fulladder_1_co, fulladder_2_co, fulladder_3_co, fulladder_4_co, xor_1_out, xor_2_out, xor_3_out,
       xor_4_out;

  xor xor_1 (xor_1_out, op, b[0]);
  FullAdder fulladder_1 (.ci(op), .in_2(xor_1_out), .in_3(a[0]), .s0(out_5[0]), .co(fulladder_1_co));
  xor xor_2 (xor_2_out, op, b[1]);
  FullAdder fulladder_2 (.ci(fulladder_1_co), .in_2(xor_2_out), .in_3(a[1]), .s0(out_5[1]), .co(fulladder_2_co));
  xor xor_3 (xor_3_out, op, b[2]);
  FullAdder fulladder_3 (.ci(fulladder_2_co), .in_2(xor_3_out), .in_3(a[2]), .s0(out_5[2]), .co(fulladder_3_co));
  xor xor_4 (xor_4_out, op, b[3]);
  FullAdder fulladder_4 (.ci(fulladder_3_co), .in_2(xor_4_out), .in_3(a[3]), .s0(out_5[3]), .co(fulladder_4_co));
  xor xor_5 (bit_Overflow, op, fulladder_4_co);
endmodule

// V0
module VerifZero (
  input  [3:0] a,
  output out_2
);

  nor nor_1 (out_2, a[3], a[2], a[1], a[0]);
endmodule

module Exemplo0032 (
  input  [3:0] a,
  input  [3:0] b,
  input  op,
  output out_4,
  output out_5
);

  wire [3:0] exemplo0031_1_out_5;

  Exemplo0031 exemplo0031_1 (.op(op), .a(a), .b(b), .out_5(exemplo0031_1_out_5), .bit_Overflow(out_4));
  VerifZero verifzero_1 (.a(exemplo0031_1_out_5), .out_2(out_5));
endmodule
