// Logisim project Exemplo0033.circ as structural Verilog: 1 circuit, main circuit main
module main (
  input  [3:0] abcd,
  output [3:0] out_2,
  output Overflow
);

  wire and_1_out, and_4_out, nor_1_out, or_1_out, xor_1_out;

  nor nor_1 (nor_1_out, abcd[0], abcd[1]);
  xor xor_1 (xor_1_out, abcd[2], abcd[0]);
  and and_1 (and_1_out, ~abcd[1], abcd[2]);  // AND_Gate
  not not_1 (out_2[0], abcd[0]);
  and and_2 (Overflow, abcd[2], abcd[1], abcd[0]);
  and and_3 (out_2[3], abcd[3], or_1_out);
  or or_1 (or_1_out, nor_1_out, ~abcd[2]);  // OR_Gate
  and and_4 (and_4_out, xor_1_out, abcd[1]);
  or or_2 (out_2[2], and_4_out, and_1_out);
  xor xor_2 (out_2[1], abcd[0], abcd[1]);
endmodule
