// Logisim project Exemplo0034.circ as structural Verilog: 1 circuit, main circuit main
module main (
  input  [3:0] in_1,
  output [3:0] out_2,
  output Overflow
);

  wire and_1_out, and_3_out, and_4_out, nor_1_out, or_1_out, or_2_out;

  or or_1 (or_1_out, in_1[0], in_1[1], in_1[2]);
  and and_1 (and_1_out, ~in_1[0], ~in_1[1], ~in_1[2], ~in_1[3]);  // AND_Gate
  or or_2 (or_2_out, in_1[0], in_1[1]);
  nor nor_1 (nor_1_out, in_1[0], in_1[1], in_1[2]);
  not not_1 (out_2[0], in_1[0]);
  and and_2 (Overflow, in_1[3], ~in_1[2], ~in_1[1], ~in_1[0]);  // AND_Gate
  and and_3 (and_3_out, in_1[3], or_1_out);
  and and_4 (and_4_out, or_2_out, in_1[2]);
  xnor xnor_1 (out_2[1], in_1[0], in_1[1]);
  or or_3 (out_2[3], and_3_out, and_1_out);
  or or_4 (out_2[2], and_4_out, nor_1_out);
endmodule
