// Logisim project Exemplo0035.circ as structural Verilog: 1 circuit, main circuit main
module main (
  input  [1:0] ab,
  input  [1:0] cd,
  output ab_cd,
  output ab_cd_2,
  output ab_cd_3
);

  wire and_1_out, and_2_out, and_3_out, and_4_out, or_1_out, or_2_out, xnor_1_out, xnor_2_out;

  or or_1 (or_1_out, ~ab[1], cd[1]);  // OR_Gate
  or or_2 (or_2_out, ab[1], ~cd[1]);  // OR_Gate
  xnor xnor_1 (xnor_1_out, ab[1], cd[1]);
  xnor xnor_2 (xnor_2_out, ab[0], cd[0]);
  and and_1 (and_1_out, or_1_out, ~ab[0], cd[0]);  // AND_Gate
  and and_2 (and_2_out, ~ab[1], cd[1]);  // AND_Gate
  and and_3 (and_3_out, or_2_out, ab[0], ~cd[0]);  // AND_Gate
  and and_4 (and_4_out, ab[1], ~cd[1]);  // AND_Gate
  and and_5 (ab_cd_3, xnor_1_out, xnor_2_out);
  or or_3 (ab_cd, and_1_out, and_2_out);
  or or_4 (ab_cd_2, and_3_out, and_4_out);
endmodule
