// Logisim project Exercicios.circ as structural Verilog
// HA
module halfAdder (
  input  x,
  input  y,
  output s0,
  output carryOut
);

  xor xor_1 (s0, y, x);
  and and_1 (carryOut, y, x);
endmodule

// FA
module fullAdder (
  input  x,
  input  y,
  input  carryIn,
  output s0,
  output carryOut
);

  wire and_1_out, and_2_out, xor_1_out;

  xor xor_1 (xor_1_out, y, x);
  and and_1 (and_1_out, y, x);
  xor xor_2 (s0, carryIn, xor_1_out);
  and and_2 (and_2_out, xor_1_out, carryIn);
  or or_1 (carryOut, and_2_out, and_1_out);
endmodule

module verifica0 (
  input  [3:0] in_1,
  output out_2
);

  nor nor_1 (out_2, in_1[0], in_1[1], in_1[2], in_1[3]);
endmodule

// SA
module Exemplo0031 (
  input  [3:0] x,
  input  [3:0] y,
  input  operador,
  output carryOut,
  output [3:0] out_5
);

  wire fulladder_1_carryout, fulladder_2_carryout, fulladder_3_carryout, xor_1_out, xor_2_out, xor_3_out,
       xor_4_out;

  xor xor_1 (xor_1_out, operador, y[0]);
  fullAdder fulladder_1 (.s0(out_5[0]), .carryOut(fulladder_1_carryout), .x(xor_1_out), .y(x[0]), .carryIn(operador));
  xor xor_2 (xor_2_out, operador, y[1]);
  fullAdder fulladder_2 (
    .s0(out_5[1]), .carryOut(fulladder_2_carryout), .x(x[1]), .y(xor_2_out), .carryIn(fulladder_1_carryout));
  xor xor_3 (xor_3_out, operador, y[2]);
  fullAdder fulladder_3 (
    .s0(out_5[2]), .carryOut(fulladder_3_carryout), .x(x[2]), .y(xor_3_out), .carryIn(fulladder_2_carryout));
  xor xor_4 (xor_4_out, operador, y[3]);
  fullAdder fulladder_4 (.s0(out_5[3]), .carryOut(carryOut), .x(x[3]), .y(xor_4_out), .carryIn(fulladder_3_carryout));
endmodule

module Exemplo0032 (
  input  [3:0] a,
  input  [3:0] b,
  input  operador,
  output carryOut,
  output out_5,
  output [3:0] s0
);

  Exemplo0031 exemplo0031_1 (.operador(operador), .x(a), .y(b), .out_5(s0), .carryOut(carryOut));
  verifica0 verifica0_1 (.in_1(s0), .out_2(out_5));
endmodule

module Exemplo0033 (
  input  [3:0] in_1,
  output [3:0] out_2,
  output overFlow
);

  wire and_1_out, and_3_out, nor_1_out, not_1_out, or_1_out, xor_1_out;

  nor nor_1 (nor_1_out, in_1[0], in_1[1]);
  not not_1 (not_1_out, in_1[2]);
  xor xor_1 (xor_1_out, in_1[0], in_1[2]);
  and and_1 (and_1_out, ~in_1[1], in_1[2]);  // AND_Gate
  xor xor_2 (out_2[1], in_1[0], in_1[1]);
  not not_2 (out_2[0], in_1[0]);
  and and_2 (overFlow, in_1[0], in_1[1], in_1[2]);
  or or_1 (or_1_out, nor_1_out, not_1_out);
  and and_3 (and_3_out, xor_1_out, in_1[1]);
  and and_4 (out_2[3], in_1[3], or_1_out);
  or or_2 (out_2[2], and_3_out, and_1_out);
endmodule

module Exemplo0034 (
  input  [3:0] in_1,
  output [3:0] out_2,
  output overFlow
);

  wire and_1_out, and_3_out, and_4_out, nor_1_out, or_1_out, or_2_out;

  or or_1 (or_1_out, in_1[0], in_1[1], in_1[2]);
  and and_1 (and_1_out, ~in_1[0], ~in_1[1], ~in_1[2], ~in_1[3]);  // AND_Gate
  or or_2 (or_2_out, in_1[0], in_1[1]);
  nor nor_1 (nor_1_out, in_1[0], in_1[1], in_1[2]);
  xnor xnor_1 (out_2[2], in_1[0], in_1[1]);
  not not_1 (out_2[3], in_1[0]);
  and and_2 (overFlow, in_1[3], ~in_1[2], ~in_1[1], ~in_1[0]);  // AND_Gate
  and and_3 (and_3_out, in_1[3], or_1_out);
  and and_4 (and_4_out, or_2_out, in_1[2]);
  or or_3 (out_2[0], and_3_out, and_1_out);
  or or_4 (out_2[1], and_4_out, nor_1_out);
endmodule

module Exemplo0035 (
  input  [1:0] w_x,
  input  [1:0] y_z,
  output wx___yz,
  output wx____yz,
  output wx___yz_2
);

  wire and_1_out, and_2_out, and_4_out, and_5_out, not_1_out, or_1_out, or_2_out, xnor_1_out, xnor_2_out;

  not not_1 (not_1_out, w_x[1]);
  or or_1 (or_1_out, not_1_out, y_z[1]);
  or or_2 (or_2_out, w_x[1], ~y_z[1]);  // OR_Gate
  and and_1 (and_1_out, or_1_out, ~w_x[0], y_z[0]);  // AND_Gate
  and and_2 (and_2_out, ~w_x[1], y_z[1]);  // AND_Gate
  xnor xnor_1 (xnor_1_out, w_x[0], y_z[0]);
  and and_3 (wx____yz, xnor_1_out, xnor_2_out);
  xnor xnor_2 (xnor_2_out, y_z[0], w_x[0]);
  and and_4 (and_4_out, or_2_out, w_x[0], ~y_z[0]);  // AND_Gate
  and and_5 (and_5_out, w_x[1], ~y_z[1]);  // AND_Gate
  or or_3 (wx___yz, and_1_out, and_2_out);
  or or_4 (wx___yz_2, and_4_out, and_5_out);
endmodule
