// Logisim project Guia05.circ as structural Verilog
module Full_Adder (
  input  a,
  input  b,
  input  c,
  output carry_out,
  output s0
);

  wire and_1_out, and_2_out, xor_2_out;

  and and_1 (and_1_out, c, xor_2_out);
  or or_1 (carry_out, and_2_out, and_1_out);
  and and_2 (and_2_out, a, b);
  xor xor_1 (s0, c, xor_2_out);
  xor xor_2 (xor_2_out, a, b);
endmodule

module Increment (
  input  carry,
  input  s2,
  input  s1,
  input  s0,
  input  inc_a,
  input  inc_b,
  output overflow,
  output s3,
  output s2_2,
  output s1_2,
  output s0_2
);

  wire full_adder_2_carry_out, full_adder_3_carry_out, full_adder_4_carry_out;

  Full_Adder full_adder_1 (.c(full_adder_2_carry_out), .a(s2), .b(1'b0), .carry_out(overflow), .s0(s3));
  Full_Adder full_adder_2 (.c(full_adder_3_carry_out), .a(s1), .b(1'b0), .carry_out(full_adder_2_carry_out), .s0(s2_2));
  Full_Adder full_adder_3 (.c(full_adder_4_carry_out), .a(s0), .b(1'b0), .carry_out(full_adder_3_carry_out), .s0(s1_2));
  Full_Adder full_adder_4 (.c(carry), .a(inc_a), .b(inc_b), .carry_out(full_adder_4_carry_out), .s0(s0_2));
endmodule

module Greater_Less (
  input  in_1,
  input  in_2,
  input  in_3,
  input  in_4,
  input  in_5,
  input  in_6,
  input  in_7,
  input  in_8,
  output a___b,
  output a___b_2
);

  wire and_1_out, and_2_out, and_3_out, and_4_out, and_5_out, and_6_out, and_7_out, and_8_out, not_1_out,
       not_2_out, not_3_out, not_4_out, not_5_out, not_6_out, not_7_out, not_8_out;

  not not_1 (not_1_out, in_1);
  and and_1 (and_1_out, not_1_out, in_5);
  and and_2 (and_2_out, in_1, not_2_out);
  not not_2 (not_2_out, in_5);
  not not_3 (not_3_out, in_2);
  and and_3 (and_3_out, not_3_out, in_6);
  and and_4 (and_4_out, in_2, not_4_out);
  not not_4 (not_4_out, in_6);
  not not_5 (not_5_out, in_3);
  and and_5 (and_5_out, not_5_out, in_7);
  and and_6 (and_6_out, in_3, not_6_out);
  not not_6 (not_6_out, in_7);
  not not_7 (not_7_out, in_4);
  and and_7 (and_7_out, not_7_out, in_8);
  and and_8 (and_8_out, in_4, not_8_out);
  not not_8 (not_8_out, in_8);
  or or_1 (a___b, and_1_out, and_3_out, and_5_out, and_7_out);
  or or_2 (a___b_2, and_2_out, and_4_out, and_6_out, and_8_out);
endmodule

module ALU1 (
  input  in_1,
  input  in_2,
  input  in_3,
  input  in_4,
  input  in_5,
  input  in_6,
  input  in_7,
  input  in_8,
  output cout,
  output s2,
  output s1,
  output s0
);

  wire full_adder_2_carry_out, full_adder_3_carry_out, xor_1_out;

  Full_Adder full_adder_1 (.c(full_adder_2_carry_out), .a(in_2), .b(in_6), .carry_out(cout), .s0(s2));
  Full_Adder full_adder_2 (.c(full_adder_3_carry_out), .a(in_3), .b(in_7), .carry_out(full_adder_2_carry_out), .s0(s1));
  Full_Adder full_adder_3 (.c(xor_1_out), .a(in_4), .b(in_8), .carry_out(full_adder_3_carry_out), .s0(s0));
  xor xor_1 (xor_1_out, in_1, in_5);
endmodule

module ALU2 (
  input  in_1,
  input  in_2,
  input  in_3,
  input  in_4,
  input  in_5,
  input  in_6,
  input  in_7,
  input  in_8,
  output equals_to_zero,
  output cout,
  output s2,
  output s1,
  output s0
);

  wire full_adder_2_carry_out, full_adder_3_carry_out, xor_1_out;

  Full_Adder full_adder_1 (.c(full_adder_2_carry_out), .a(in_2), .b(in_6), .carry_out(cout), .s0(s2));
  Full_Adder full_adder_2 (.c(full_adder_3_carry_out), .a(in_3), .b(in_7), .carry_out(full_adder_2_carry_out), .s0(s1));
  nor nor_1 (equals_to_zero, s0, s1, s2, cout);
  Full_Adder full_adder_3 (.c(xor_1_out), .a(in_4), .b(in_8), .carry_out(full_adder_3_carry_out), .s0(s0));
  xor xor_1 (xor_1_out, in_1, in_5);
endmodule

module ALU3 (
  input  in_1,
  input  in_2,
  input  in_3,
  input  in_4,
  input  in_5,
  input  in_6,
  input  in_7,
  input  in_8,
  input  increment_a,
  input  increment_b,
  output s2,
  output s1,
  output inc,
  output s0,
  output overflow
);

  wire full_adder_1_carry_out, full_adder_1_s0, full_adder_2_carry_out, full_adder_2_s0,
       full_adder_3_carry_out, full_adder_3_s0, xor_1_out;

  Full_Adder full_adder_1 (
    .c(full_adder_2_carry_out), .a(in_2), .b(in_6), .carry_out(full_adder_1_carry_out), .s0(full_adder_1_s0));
  Full_Adder full_adder_2 (
    .c(full_adder_3_carry_out), .a(in_3), .b(in_7), .carry_out(full_adder_2_carry_out), .s0(full_adder_2_s0));
  Full_Adder full_adder_3 (.c(xor_1_out), .a(in_4), .b(in_8), .carry_out(full_adder_3_carry_out), .s0(full_adder_3_s0));
  Increment increment_1 (
    .carry(full_adder_1_carry_out), .s2(full_adder_1_s0), .s1(full_adder_2_s0), .s0(full_adder_3_s0),
    .inc_a(increment_a), .inc_b(increment_b), .overflow(overflow), .s2_2(s1), .s1_2(s0), .s0_2(inc), .s3(s2));
  xor xor_1 (xor_1_out, in_1, in_5);
endmodule

module ALU5 (
  input  in_1,
  input  in_2,
  input  in_3,
  input  in_4,
  input  in_5,
  input  in_6,
  input  in_7,
  input  in_8,
  input  increment_a,
  input  increment_b,
  output overflow,
  output a_b,
  output a_b_2,
  output equals_to_zero,
  output cout,
  output s2,
  output s1,
  output s0
);

  wire full_adder_1_carry_out, full_adder_1_s0, full_adder_2_carry_out, full_adder_2_s0,
       full_adder_3_carry_out, full_adder_3_s0, xor_1_out;

  Full_Adder full_adder_1 (
    .c(full_adder_2_carry_out), .a(in_2), .b(in_6), .carry_out(full_adder_1_carry_out), .s0(full_adder_1_s0));
  Full_Adder full_adder_2 (
    .c(full_adder_3_carry_out), .a(in_3), .b(in_7), .carry_out(full_adder_2_carry_out), .s0(full_adder_2_s0));
  nor nor_1 (equals_to_zero, s0, s1, s2, cout);
  Greater_Less greater_less_1 (
    .in_1(in_1), .in_2(in_2), .in_3(in_3), .in_4(in_4), .in_5(in_5), .in_6(in_6), .in_7(in_7), .in_8(in_8),
    .a___b(a_b), .a___b_2(a_b_2));
  Full_Adder full_adder_3 (.c(xor_1_out), .a(in_4), .b(in_8), .carry_out(full_adder_3_carry_out), .s0(full_adder_3_s0));
  Increment increment_1 (
    .carry(full_adder_1_carry_out), .s2(full_adder_1_s0), .s1(full_adder_2_s0), .s0(full_adder_3_s0),
    .inc_a(increment_a), .inc_b(increment_b), .overflow(overflow), .s2_2(s2), .s1_2(s1), .s0_2(s0), .s3(cout));
  xor xor_1 (xor_1_out, in_1, in_5);
endmodule
