// Logisim project Guia5.circ as structural Verilog: 12 circuits, main circuit Soma Completa
// FA
module Soma_Completa (
  input  A,
  input  B,
  input  Carry_In,
  output S0,
  output Carry_Out
);

  wire and_1_out, and_2_out, xor_1_out, xor_2_out;

  xor xor_1 (xor_1_out, A, B);
  and and_1 (and_1_out, A, B);
  xor xor_2 (xor_2_out, A, B);
  and and_2 (and_2_out, Carry_In, xor_1_out);
  xor xor_3 (S0, xor_2_out, Carry_In);
  or or_1 (Carry_Out, and_2_out, and_1_out);
endmodule

module Diferenca_Completa (
  input  A,
  input  B,
  input  Carry_In,
  output S0,
  output Carry_Out
);

  wire and_1_out, and_2_out, not_1_out, not_2_out, or_1_out;

  xor xor_1 (S0, A, B);
  not not_1 (not_1_out, A);
  or or_1 (or_1_out, not_1_out, B);
  and and_1 (and_1_out, or_1_out, Carry_In);
  not not_2 (not_2_out, A);
  and and_2 (and_2_out, not_2_out, B);
  or or_2 (Carry_Out, and_1_out, and_2_out);
endmodule

// FA 4 bits
module Exercicio_1a (
  input  A,
  input  B,
  input  C,
  input  D,
  input  Carry_In,
  input  X,
  input  Y,
  input  Z,
  input  W,
  output snl,
  output s3,
  output s2,
  output s1,
  output s0
);

  wire soma_completa_1_carry_out, soma_completa_2_carry_out, soma_completa_3_carry_out;

  Soma_Completa soma_completa_1 (.A(D), .B(W), .Carry_In(Carry_In), .S0(s0), .Carry_Out(soma_completa_1_carry_out));
  Soma_Completa soma_completa_2 (
    .A(C), .B(Z), .Carry_In(soma_completa_1_carry_out), .S0(s1), .Carry_Out(soma_completa_2_carry_out));
  Soma_Completa soma_completa_3 (
    .A(B), .B(Y), .Carry_In(soma_completa_2_carry_out), .S0(s2), .Carry_Out(soma_completa_3_carry_out));
  Soma_Completa soma_completa_4 (.A(A), .B(X), .Carry_In(soma_completa_3_carry_out), .S0(s3), .Carry_Out(snl));
endmodule

// SUB 4 Bits
module Exercicio_2a (
  input  A,
  input  B,
  input  C,
  input  D,
  input  X,
  input  Y,
  input  Z,
  input  W,
  input  Carry_In,
  output snl,
  output s3,
  output s2,
  output s1,
  output s0
);

  wire diferenca_completa_1_carry_out, diferenca_completa_2_carry_out, diferenca_completa_3_carry_out;

  Diferenca_Completa diferenca_completa_1 (
    .A(D), .B(W), .Carry_In(Carry_In), .S0(s0), .Carry_Out(diferenca_completa_1_carry_out));
  Diferenca_Completa diferenca_completa_2 (
    .A(C), .B(Z), .Carry_In(diferenca_completa_1_carry_out), .S0(s1),
    .Carry_Out(diferenca_completa_2_carry_out));
  Diferenca_Completa diferenca_completa_3 (
    .A(B), .B(Y), .Carry_In(diferenca_completa_2_carry_out), .S0(s2),
    .Carry_Out(diferenca_completa_3_carry_out));
  Diferenca_Completa diferenca_completa_4 (
    .A(A), .B(X), .Carry_In(diferenca_completa_3_carry_out), .S0(s3), .Carry_Out(snl));
endmodule

module Exercicio_3a (
  input  [3:0] A,
  input  [3:0] B
);

  wire and_1_out, not_1_out, not_2_out, not_3_out, not_4_out, xor_1_out, xor_2_out, xor_3_out, xor_4_out;

  not not_1 (not_1_out, xor_1_out);
  xor xor_1 (xor_1_out, A[3], B[3]);
  xor xor_2 (xor_2_out, A[2], B[2]);
  not not_2 (not_2_out, xor_2_out);
  not not_3 (not_3_out, xor_3_out);
  xor xor_3 (xor_3_out, A[1], B[1]);
  not not_4 (not_4_out, xor_4_out);
  xor xor_4 (xor_4_out, A[0], B[0]);
  and and_1 (and_1_out, not_1_out, not_2_out, not_3_out, not_4_out);
  // Probe on and_1_out
endmodule

module Exercicio_4a (
  input  [3:0] A,
  input  [3:0] B
);

  wire or_1_out, xor_1_out, xor_2_out, xor_3_out, xor_4_out;

  xor xor_1 (xor_1_out, A[3], B[3]);
  xor xor_2 (xor_2_out, A[2], B[2]);
  xor xor_3 (xor_3_out, A[1], B[1]);
  xor xor_4 (xor_4_out, A[0], B[0]);
  or or_1 (or_1_out, xor_1_out, xor_2_out, xor_3_out, xor_4_out);
  // Probe on or_1_out
endmodule

// C2 4bits
module Exercicio_5a (
  input  X,
  input  Y,
  input  Z,
  input  W,
  output out_5,
  output out_6,
  output out_7,
  output out_8,
  output out_9
);

  wire exercicio_2a_1_s0, exercicio_2a_1_s1, exercicio_2a_1_s2, exercicio_2a_1_s3, exercicio_2a_1_snl;

  Exercicio_2a exercicio_2a_1 (
    .Carry_In(1'b0), .A(1'b1), .X(X), .B(1'b1), .Y(Y), .C(1'b1), .Z(Z), .D(1'b1), .W(W),
    .snl(exercicio_2a_1_snl), .s3(exercicio_2a_1_s3), .s2(exercicio_2a_1_s2), .s1(exercicio_2a_1_s1),
    .s0(exercicio_2a_1_s0));
  Exercicio_1a exercicio_1a_1 (
    .A(exercicio_2a_1_s3), .B(exercicio_2a_1_s2), .C(exercicio_2a_1_s1), .D(exercicio_2a_1_s0), .X(1'b0),
    .Y(1'b0), .Z(1'b0), .W(1'b1), .Carry_In(exercicio_2a_1_snl), .snl(out_5), .s3(out_6), .s2(out_7),
    .s1(out_8), .s0(out_9));
endmodule

module Exemplo0031 (
  input  in_1,
  input  [3:0] in_2,
  input  [3:0] in_3,
  input  in_4,
  input  in_5
);

  wire [4:0] and_1_out, and_2_out, exercicio_1a_1_s0, exercicio_2a_1_s0, or_1_out;
  wire [4:4] not_1_out;

  Exercicio_2a exercicio_2a_1 (
    .Carry_In(in_4), .A(in_2[3]), .X(in_3[3]), .B(in_2[2]), .Y(in_3[2]), .C(in_2[1]), .Z(in_3[1]),
    .D(in_2[0]), .W(in_3[0]), .snl(exercicio_2a_1_s0[4]), .s3(exercicio_2a_1_s0[3]),
    .s2(exercicio_2a_1_s0[2]), .s1(exercicio_2a_1_s0[1]), .s0(exercicio_2a_1_s0[0]));
  assign and_1_out = {5{in_5}} & exercicio_2a_1_s0;  // AND_Gate and_1, 5 bits wide
  not not_1 (not_1_out[4], in_5);
  assign or_1_out = and_1_out | and_2_out;  // OR_Gate or_1, 5 bits wide
  // Probe on or_1_out
  Exercicio_1a exercicio_1a_1 (
    .A(in_2[3]), .B(in_2[2]), .C(in_2[1]), .D(in_2[0]), .X(in_3[3]), .Y(in_3[2]), .Z(in_3[1]), .W(in_3[0]),
    .Carry_In(in_1), .snl(exercicio_1a_1_s0[4]), .s3(exercicio_1a_1_s0[3]), .s2(exercicio_1a_1_s0[2]),
    .s1(exercicio_1a_1_s0[1]), .s0(exercicio_1a_1_s0[0]));
  assign and_2_out = {5{not_1_out[4]}} & exercicio_1a_1_s0;  // AND_Gate and_2, 5 bits wide
endmodule

module Exemplo0032 (
  input  in_1,
  input  [3:0] in_2,
  input  [3:0] in_3,
  input  in_4,
  input  in_5,
  input  in_6
);

  wire nor_1_out;
  wire [4:0] and_1_out, and_2_out, exercicio_1a_1_s0, exercicio_2a_1_s0, or_1_out;
  wire [4:4] not_1_out;

  assign and_1_out = {5{in_5}} & exercicio_2a_1_s0;  // AND_Gate and_1, 5 bits wide
  Exercicio_2a exercicio_2a_1 (
    .Carry_In(in_4), .A(in_2[3]), .X(in_3[3]), .B(in_2[2]), .Y(in_3[2]), .C(in_2[1]), .Z(in_3[1]),
    .D(in_2[0]), .W(in_3[0]), .snl(exercicio_2a_1_s0[4]), .s3(exercicio_2a_1_s0[3]),
    .s2(exercicio_2a_1_s0[2]), .s1(exercicio_2a_1_s0[1]), .s0(exercicio_2a_1_s0[0]));
  // Probe on or_1_out
  nor nor_1 (nor_1_out, or_1_out[4], or_1_out[3], or_1_out[2], or_1_out[1], or_1_out[0], in_6);
  // Probe on nor_1_out
  not not_1 (not_1_out[4], in_5);
  assign or_1_out = and_1_out | and_2_out;  // OR_Gate or_1, 5 bits wide
  Exercicio_1a exercicio_1a_1 (
    .A(in_2[3]), .B(in_2[2]), .C(in_2[1]), .D(in_2[0]), .X(in_3[3]), .Y(in_3[2]), .Z(in_3[1]), .W(in_3[0]),
    .Carry_In(in_1), .snl(exercicio_1a_1_s0[4]), .s3(exercicio_1a_1_s0[3]), .s2(exercicio_1a_1_s0[2]),
    .s1(exercicio_1a_1_s0[1]), .s0(exercicio_1a_1_s0[0]));
  assign and_2_out = {5{not_1_out[4]}} & exercicio_1a_1_s0;  // AND_Gate and_2, 5 bits wide
endmodule

module Exemplo0033 (
  input  in_1,
  input  in_2,
  input  in_3,
  input  in_4,
  input  in_5,
  input  in_6,
  input  in_7,
  input  in_8,
  output out_9,
  output out_10,
  output out_11,
  output out_12,
  output out_13
);

  Exercicio_1a exercicio_1a_1 (
    .A(in_1), .B(in_2), .C(in_3), .D(in_4), .X(in_5), .Y(in_6), .Z(in_7), .W(in_8), .Carry_In(1'b1),
    .snl(out_9), .s3(out_10), .s2(out_11), .s1(out_12), .s0(out_13));
endmodule

module Exemplo0034 (
  input  A,
  input  B,
  input  C,
  input  D
);

  wire diferenca_completa_1_carry_out, diferenca_completa_1_s0, diferenca_completa_2_carry_out,
       diferenca_completa_2_s0, diferenca_completa_3_carry_out, diferenca_completa_3_s0,
       diferenca_completa_4_carry_out, diferenca_completa_4_s0, not_1_out;

  not not_1 (not_1_out, 1'b0);
  Diferenca_Completa diferenca_completa_1 (
    .A(A), .B(1'b0), .Carry_In(1'b0), .S0(diferenca_completa_1_s0), .Carry_Out(diferenca_completa_1_carry_out));
  Diferenca_Completa diferenca_completa_2 (
    .A(B), .B(1'b0), .Carry_In(diferenca_completa_1_carry_out), .S0(diferenca_completa_2_s0),
    .Carry_Out(diferenca_completa_2_carry_out));
  Diferenca_Completa diferenca_completa_3 (
    .A(C), .B(1'b0), .Carry_In(diferenca_completa_2_carry_out), .S0(diferenca_completa_3_s0),
    .Carry_Out(diferenca_completa_3_carry_out));
  Diferenca_Completa diferenca_completa_4 (
    .A(D), .B(not_1_out), .Carry_In(diferenca_completa_3_carry_out), .S0(diferenca_completa_4_s0),
    .Carry_Out(diferenca_completa_4_carry_out));
  // Probe on diferenca_completa_1_s0
  // Probe on diferenca_completa_2_s0
  // Probe on diferenca_completa_4_carry_out
  // Probe on diferenca_completa_4_s0
  // Probe on diferenca_completa_3_s0
endmodule

module Exemplo0035___Comparador (
  input  [3:0] in_1,
  input  [3:0] in_2,
  input  in_3
);

  wire and_1_out, and_2_out, exercicio_2a_1_s0, exercicio_2a_1_s1, exercicio_2a_1_s2, exercicio_2a_1_s3,
       exercicio_2a_1_snl, nor_1_out, not_1_out, not_2_out, not_3_out;

  Exercicio_2a exercicio_2a_1 (
    .Carry_In(in_3), .A(in_1[3]), .X(in_2[3]), .B(in_1[2]), .Y(in_2[2]), .C(in_1[1]), .Z(in_2[1]),
    .D(in_1[0]), .W(in_2[0]), .snl(exercicio_2a_1_snl), .s3(exercicio_2a_1_s3), .s2(exercicio_2a_1_s2),
    .s1(exercicio_2a_1_s1), .s0(exercicio_2a_1_s0));
  nor nor_1 (nor_1_out, exercicio_2a_1_snl, exercicio_2a_1_s3, exercicio_2a_1_s2, exercicio_2a_1_s1, exercicio_2a_1_s0);
  not not_1 (not_1_out, nor_1_out);
  not not_2 (not_2_out, exercicio_2a_1_snl);
  not not_3 (not_3_out, nor_1_out);
  and and_1 (and_1_out, not_1_out, not_2_out);
  and and_2 (and_2_out, not_3_out, exercicio_2a_1_snl);
  // Probe on and_1_out
  // Probe on nor_1_out
  // Probe on and_2_out
endmodule
