// Logisim project Exemplo0033.circ as structural Verilog: 1 circuit, main circuit main
module main (
  input  [1:0] A,
  input  [1:0] B,
  input  [1:0] C,
  output [1:0] S0,
  output [1:0] S1
);

  wire [1:0] AND0_out, AND1_out, AND2_out, AND3_out, AND4_out, NAND_0_out, NOR0_out, NOT1_out, NOT2_out,
       OR0_out;

  assign NAND_0_out = ~(A & B);  // NAND_Gate NAND_0, 2 bits wide
  assign NOR0_out = ~(A | B);  // NOR_Gate NOR0, 2 bits wide
  assign AND0_out = A & B;  // AND_Gate AND0, 2 bits wide
  assign OR0_out = A | B;  // OR_Gate OR0, 2 bits wide
  assign NOT1_out = ~C;  // NOT_Gate NOT1, 2 bits wide
  assign NOT2_out = ~C;  // NOT_Gate NOT2, 2 bits wide
  assign AND1_out = NAND_0_out & C;  // AND_Gate AND1, 2 bits wide
  assign AND2_out = NOR0_out & C;  // AND_Gate AND2, 2 bits wide
  assign AND3_out = AND0_out & NOT1_out;  // AND_Gate AND3, 2 bits wide
  assign AND4_out = OR0_out & NOT2_out;  // AND_Gate AND4, 2 bits wide
  assign S0 = AND1_out | AND3_out;  // OR_Gate OR1, 2 bits wide
  assign S1 = AND2_out | AND4_out;  // OR_Gate OR2, 2 bits wide

  // Notes on the sheet:
  //   0-OR/AND
  //   /1-NAND/NOR
endmodule
