// Logisim project Exemplo0036.circ as structural Verilog: 1 circuit, main circuit main
module main (
  input  [3:0] A,
  input  [3:0] B,
  input  C,
  output S0,
  output S1
);

  wire or1_out, xor1_out, xor2_out, xor3_out, xor4_out;

  xor xor1 (xor1_out, B[0], A[0]);
  xor xor2 (xor2_out, A[1], B[1]);
  xor xor3 (xor3_out, A[2], B[2]);
  xor xor4 (xor4_out, A[3], B[3]);
  nor nor1 (S0, xor1_out, xor2_out, xor3_out, xor4_out, C);
  or or1 (or1_out, xor1_out, xor2_out, xor3_out, xor4_out);
  and nand2 (S1, C, or1_out);

  // Notes on the sheet:
  //   0-IGUAL
  //   1-DIFERENTE
endmodule
