// Logisim project Exercicios Logisim.circ as structural Verilog: 11 circuits, main circuit Full Adder
// FAx4
module Exemplo0031 (
  input  [3:0] a,
  input  [3:0] b,
  input  Carry_in,
  output Carry_out,
  output [3:0] s
);

  wire full_adder_1_carry_out, full_adder_2_carry_out, full_adder_3_carry_out, full_adder_4_carry_out;
  wire [3:0] xor_2_out;

  xor xor_1 (Carry_out, Carry_in, full_adder_1_carry_out);
  Full_Adder full_adder_1 (
    .carry_in(full_adder_2_carry_out), .carry_out(full_adder_1_carry_out), .a(a[3]), .b(xor_2_out[3]),
    .s(s[3]));
  Full_Adder full_adder_2 (
    .carry_in(full_adder_3_carry_out), .carry_out(full_adder_2_carry_out), .a(a[2]), .b(xor_2_out[2]),
    .s(s[2]));
  Full_Adder full_adder_3 (
    .carry_in(full_adder_4_carry_out), .carry_out(full_adder_3_carry_out), .a(a[1]), .b(xor_2_out[1]),
    .s(s[1]));
  assign xor_2_out = b ^ {4{Carry_in}};  // XOR_Gate xor_2, 4 bits wide
  Full_Adder full_adder_4 (
    .carry_in(Carry_in), .carry_out(full_adder_4_carry_out), .a(a[0]), .b(xor_2_out[0]), .s(s[0]));
endmodule

module Exemplo0032 (
  input  [3:0] a,
  input  [3:0] b,
  input  Carry_in,
  output Carry_out,
  output Equals_0,
  output [3:0] s
);

  wire equals_0_1_s, equals_0_2_s, equals_0_3_s, equals_0_4_s, full_adder_1_carry_out,
       full_adder_2_carry_out, full_adder_3_carry_out, full_adder_4_carry_out;
  wire [3:0] xor_2_out;

  xor xor_1 (Carry_out, Carry_in, full_adder_2_carry_out);
  Full_Adder full_adder_1 (
    .carry_in(full_adder_3_carry_out), .carry_out(full_adder_1_carry_out), .a(a[2]), .b(xor_2_out[2]),
    .s(s[2]));
  Full_Adder full_adder_2 (
    .carry_in(full_adder_1_carry_out), .carry_out(full_adder_2_carry_out), .a(a[3]), .b(xor_2_out[3]),
    .s(s[3]));
  Full_Adder full_adder_3 (
    .carry_in(full_adder_4_carry_out), .carry_out(full_adder_3_carry_out), .a(a[1]), .b(xor_2_out[1]),
    .s(s[1]));
  assign xor_2_out = b ^ {4{Carry_in}};  // XOR_Gate xor_2, 4 bits wide
  Full_Adder full_adder_4 (
    .carry_in(Carry_in), .carry_out(full_adder_4_carry_out), .a(a[0]), .b(xor_2_out[0]), .s(s[0]));
  Equals_0 equals_0_1 (.in_1(s[0]), .s(equals_0_1_s));
  Equals_0 equals_0_2 (.in_1(s[1]), .s(equals_0_2_s));
  Equals_0 equals_0_3 (.in_1(s[2]), .s(equals_0_3_s));
  Equals_0 equals_0_4 (.in_1(s[3]), .s(equals_0_4_s));
  and and_1 (Equals_0, equals_0_1_s, equals_0_2_s, equals_0_3_s, equals_0_4_s);

  // Notes on the sheet:
  //   Julio Machado - 435666
endmodule

module Exemplo0033 (
  input  [3:0] a,
  input  [3:0] b,
  input  Carry_in,
  output Carry_out,
  output Teste,
  output [3:0] s
);

  wire equals_0_1_s, equals_0_2_s, equals_0_3_s, equals_0_4_s, full_adder_1_carry_out,
       full_adder_2_carry_out, full_adder_3_carry_out, full_adder_4_carry_out;
  wire [3:0] plus_minus_1_1_s, xor_2_out;

  xor xor_1 (Carry_out, Carry_in, full_adder_2_carry_out);
  Plus___Minus_1 plus_minus_1_1 (._0____1____1____1(1'b0), .a(a), .s(plus_minus_1_1_s));
  Full_Adder full_adder_1 (
    .carry_in(full_adder_3_carry_out), .carry_out(full_adder_1_carry_out), .a(plus_minus_1_1_s[2]),
    .b(xor_2_out[2]), .s(s[2]));
  Full_Adder full_adder_2 (
    .carry_in(full_adder_1_carry_out), .carry_out(full_adder_2_carry_out), .a(plus_minus_1_1_s[3]),
    .b(xor_2_out[3]), .s(s[3]));
  Full_Adder full_adder_3 (
    .carry_in(full_adder_4_carry_out), .carry_out(full_adder_3_carry_out), .a(plus_minus_1_1_s[1]),
    .b(xor_2_out[1]), .s(s[1]));
  assign xor_2_out = b ^ {4{Carry_in}};  // XOR_Gate xor_2, 4 bits wide
  Full_Adder full_adder_4 (
    .carry_in(Carry_in), .carry_out(full_adder_4_carry_out), .a(plus_minus_1_1_s[0]), .b(xor_2_out[0]),
    .s(s[0]));
  Equals_0 equals_0_1 (.in_1(s[0]), .s(equals_0_1_s));
  Equals_0 equals_0_2 (.in_1(s[1]), .s(equals_0_2_s));
  Equals_0 equals_0_3 (.in_1(s[2]), .s(equals_0_3_s));
  Equals_0 equals_0_4 (.in_1(s[3]), .s(equals_0_4_s));
  and and_1 (Teste, equals_0_1_s, equals_0_2_s, equals_0_3_s, equals_0_4_s);

  // Notes on the sheet:
  //   JULIO MACHADO - 435666
endmodule

module Exemplo0034 (
  input  [3:0] a,
  input  [3:0] b,
  input  Carry_in,
  output Carry_out,
  output Teste,
  output [3:0] s
);

  wire equals_0_1_s, equals_0_2_s, equals_0_3_s, equals_0_4_s, full_adder_1_carry_out,
       full_adder_2_carry_out, full_adder_3_carry_out, full_adder_4_carry_out;
  wire [3:0] plus_minus_1_1_s, xor_2_out;

  xor xor_1 (Carry_out, Carry_in, full_adder_1_carry_out);
  Plus___Minus_1 plus_minus_1_1 (._0____1____1____1(1'b1), .a(a), .s(plus_minus_1_1_s));
  Full_Adder full_adder_1 (
    .carry_in(full_adder_2_carry_out), .carry_out(full_adder_1_carry_out), .a(plus_minus_1_1_s[3]),
    .b(xor_2_out[3]), .s(s[3]));
  Full_Adder full_adder_2 (
    .carry_in(full_adder_3_carry_out), .carry_out(full_adder_2_carry_out), .a(plus_minus_1_1_s[2]),
    .b(xor_2_out[2]), .s(s[2]));
  Full_Adder full_adder_3 (
    .carry_in(full_adder_4_carry_out), .carry_out(full_adder_3_carry_out), .a(plus_minus_1_1_s[1]),
    .b(xor_2_out[1]), .s(s[1]));
  assign xor_2_out = b ^ {4{Carry_in}};  // XOR_Gate xor_2, 4 bits wide
  Full_Adder full_adder_4 (
    .carry_in(Carry_in), .carry_out(full_adder_4_carry_out), .a(plus_minus_1_1_s[0]), .b(xor_2_out[0]),
    .s(s[0]));
  Equals_0 equals_0_1 (.in_1(s[0]), .s(equals_0_1_s));
  Equals_0 equals_0_2 (.in_1(s[1]), .s(equals_0_2_s));
  Equals_0 equals_0_3 (.in_1(s[2]), .s(equals_0_3_s));
  Equals_0 equals_0_4 (.in_1(s[3]), .s(equals_0_4_s));
  and and_1 (Teste, equals_0_1_s, equals_0_2_s, equals_0_3_s, equals_0_4_s);

  // Notes on the sheet:
  //   JULIO MACHADO - 435666
endmodule

module Exemplo0035 (
  input  [3:0] a,
  input  [3:0] b,
  output A___B,
  output A___B_2
);

  wire [2:0] exemplo0031_1_s;

  Exemplo0031 exemplo0031_1 (.Carry_in(1'b1), .a(a), .b(b), .s({A___B, exemplo0031_1_s}));  // open: Carry_out
  not not_1 (A___B_2, A___B);

  // Notes on the sheet:
  //   JULIO MACHADO - 435666
endmodule

module Exemplo0036 (
  input  [3:0] a,
  input  [3:0] b,
  input  _0____1____1____1,
  input  Carry_in,
  output Overflow,
  output Teste,
  output [3:0] s
);

  wire equals_0_1_s, equals_0_2_s, equals_0_3_s, equals_0_4_s, full_adder_1_carry_out,
       full_adder_2_carry_out, full_adder_3_carry_out, full_adder_4_carry_out;
  wire [3:0] plus_minus_1_1_s, xor_2_out;

  xor xor_1 (Overflow, Carry_in, full_adder_1_carry_out);
  Plus___Minus_1 plus_minus_1_1 (._0____1____1____1(_0____1____1____1), .a(a), .s(plus_minus_1_1_s));
  Full_Adder full_adder_1 (
    .carry_in(full_adder_2_carry_out), .carry_out(full_adder_1_carry_out), .a(plus_minus_1_1_s[3]),
    .b(xor_2_out[3]), .s(s[3]));
  Full_Adder full_adder_2 (
    .carry_in(full_adder_3_carry_out), .carry_out(full_adder_2_carry_out), .a(plus_minus_1_1_s[2]),
    .b(xor_2_out[2]), .s(s[2]));
  Full_Adder full_adder_3 (
    .carry_in(full_adder_4_carry_out), .carry_out(full_adder_3_carry_out), .a(plus_minus_1_1_s[1]),
    .b(xor_2_out[1]), .s(s[1]));
  assign xor_2_out = b ^ {4{Carry_in}};  // XOR_Gate xor_2, 4 bits wide
  Full_Adder full_adder_4 (
    .carry_in(Carry_in), .carry_out(full_adder_4_carry_out), .a(plus_minus_1_1_s[0]), .b(xor_2_out[0]),
    .s(s[0]));
  Equals_0 equals_0_1 (.in_1(s[0]), .s(equals_0_1_s));
  Equals_0 equals_0_2 (.in_1(s[1]), .s(equals_0_2_s));
  Equals_0 equals_0_3 (.in_1(s[2]), .s(equals_0_3_s));
  Equals_0 equals_0_4 (.in_1(s[3]), .s(equals_0_4_s));
  and and_1 (Teste, equals_0_1_s, equals_0_2_s, equals_0_3_s, equals_0_4_s);

  // Notes on the sheet:
  //   JULIO MACHADO - 435666
endmodule

module Exemplo0037 (
  input  [3:0] a,
  input  [3:0] b,
  input  _0____1____1____1,
  input  Carry_in,
  output Carry_out,
  output Teste,
  output [3:0] s
);

  wire equals_0_1_s, equals_0_2_s, equals_0_3_s, equals_0_4_s, full_adder_1_carry_out,
       full_adder_2_carry_out, full_adder_3_carry_out, full_adder_4_carry_out;
  wire [3:0] plus_minus_1_1_s, xor_2_out;

  xor xor_1 (Carry_out, Carry_in, full_adder_2_carry_out);
  Plus___Minus_1 plus_minus_1_1 (._0____1____1____1(_0____1____1____1), .a(a), .s(plus_minus_1_1_s));
  Full_Adder full_adder_1 (
    .carry_in(full_adder_3_carry_out), .carry_out(full_adder_1_carry_out), .a(plus_minus_1_1_s[2]),
    .b(xor_2_out[2]), .s(s[2]));
  Full_Adder full_adder_2 (
    .carry_in(full_adder_1_carry_out), .carry_out(full_adder_2_carry_out), .a(plus_minus_1_1_s[3]),
    .b(xor_2_out[3]), .s(s[3]));
  Full_Adder full_adder_3 (
    .carry_in(full_adder_4_carry_out), .carry_out(full_adder_3_carry_out), .a(plus_minus_1_1_s[1]),
    .b(xor_2_out[1]), .s(s[1]));
  assign xor_2_out = b ^ {4{Carry_in}};  // XOR_Gate xor_2, 4 bits wide
  Full_Adder full_adder_4 (
    .carry_in(Carry_in), .carry_out(full_adder_4_carry_out), .a(plus_minus_1_1_s[0]), .b(xor_2_out[0]),
    .s(s[0]));
  Equals_0 equals_0_1 (.in_1(s[0]), .s(equals_0_1_s));
  Equals_0 equals_0_2 (.in_1(s[1]), .s(equals_0_2_s));
  Equals_0 equals_0_3 (.in_1(s[2]), .s(equals_0_3_s));
  Equals_0 equals_0_4 (.in_1(s[3]), .s(equals_0_4_s));
  and and_1 (Teste, equals_0_1_s, equals_0_2_s, equals_0_3_s, equals_0_4_s);

  // Notes on the sheet:
  //   JULIO MACHADO - 435666
endmodule

// T.I
module Equals_0 (
  input  in_1,
  output s
);

  nor nor_1 (s, in_1, 1'b0);
endmodule

// +/- 1
module Plus___Minus_1 (
  input  [3:0] a,
  input  _0____1____1____1,
  output [3:0] s
);

  wire exemplo0031_1_carry_out;

  Exemplo0031 exemplo0031_1 (
    .Carry_out(exemplo0031_1_carry_out), .Carry_in(_0____1____1____1), .a(a), .b(4'b0001), .s(s));
endmodule

// 4bit F.A
module _4bits_Full_Adder (
  input  a_3,
  input  a_2,
  input  a_1,
  input  a_0,
  input  b_3,
  input  b_2,
  input  b_1,
  input  b_0,
  input  Carry_in,
  output Carry_out,
  output [3:0] s
);

  wire full_adder_2_carry_out, full_adder_3_carry_out, full_adder_4_carry_out;

  Full_Adder full_adder_1 (.carry_in(full_adder_2_carry_out), .carry_out(Carry_out), .a(a_3), .b(b_3), .s(s[3]));
  Full_Adder full_adder_2 (
    .carry_in(full_adder_3_carry_out), .carry_out(full_adder_2_carry_out), .a(a_2), .b(b_2), .s(s[2]));
  Full_Adder full_adder_3 (
    .carry_in(full_adder_4_carry_out), .carry_out(full_adder_3_carry_out), .a(a_1), .b(b_1), .s(s[1]));
  Full_Adder full_adder_4 (.carry_in(Carry_in), .carry_out(full_adder_4_carry_out), .a(a_0), .b(b_0), .s(s[0]));

  // Notes on the sheet:
  //   Julio Machado - 435666
endmodule

// F.A
module Full_Adder (
  input  a,
  input  b,
  input  carry_in,
  output carry_out,
  output s
);

  wire and_1_out, and_2_out, xor_1_out;

  xor xor_1 (xor_1_out, b, a);
  and and_1 (and_1_out, a, b);
  and and_2 (and_2_out, xor_1_out, carry_in);
  xor xor_2 (s, carry_in, xor_1_out);
  or or_1 (carry_out, and_2_out, and_1_out);

  // Notes on the sheet:
  //   Julio Machado - 435666
endmodule
