// Logisim project Exemplo0034.circ as structural Verilog: 3 circuits, main circuit Exemplo0034
module Exemplo0034 (
  input  a3,
  input  a2,
  input  a1,
  input  a0,
  input  b3,
  input  b2,
  input  b1,
  input  b0,
  input  Carry_in,
  output Carry_out,
  output s3,
  output s2,
  output s1,
  output s0,
  output Detector_de_zero
);

  wire fulladder_1_out_5, fulladder_2_out_5, fulladder_3_out_5, fulladder_4_out_5, not_1_out, XOR_2_out,
       XOR_3_out, XOR_4_out, XOR_5_out;

  xor XOR (Carry_out, Carry_in, fulladder_1_out_5);
  xor XOR_2 (XOR_2_out, b3, Carry_in);
  FullAdder fulladder_1 (.out_5(fulladder_1_out_5), .in_1(a3), .in_2(XOR_2_out), .out_4(s3), .in_3(fulladder_2_out_5));
  xor XOR_3 (XOR_3_out, b2, Carry_in);
  FullAdder fulladder_2 (.out_5(fulladder_2_out_5), .in_1(a2), .in_2(XOR_3_out), .out_4(s2), .in_3(fulladder_3_out_5));
  xor XOR_4 (XOR_4_out, b1, Carry_in);
  FullAdder fulladder_3 (.out_5(fulladder_3_out_5), .in_1(a1), .in_2(XOR_4_out), .out_4(s1), .in_3(fulladder_4_out_5));
  xor XOR_5 (XOR_5_out, b0, Carry_in);
  FullAdder fulladder_4 (.out_5(fulladder_4_out_5), .in_1(a0), .in_2(XOR_5_out), .out_4(s0), .in_3(not_1_out));
  not not_1 (not_1_out, 1'b1);
  nor NOR (Detector_de_zero, Carry_out, s3, s2, s1, s0);

  // Notes on the sheet:
  //   Exemplo0034
  //   0 - NÃO
  //   1 - SIM
endmodule

// HA
module HalfAdder (
  input  a,
  input  b,
  output s0,
  output s1
);

  xor XOR (s0, a, b);
  and AND (s1, a, b);
endmodule

// FA
module FullAdder (
  input  in_1,
  input  in_2,
  input  in_3,
  output out_4,
  output out_5
);

  wire halfadder_1_s0, halfadder_1_s1, halfadder_2_s1;

  HalfAdder halfadder_1 (.a(in_1), .b(in_2), .s0(halfadder_1_s0), .s1(halfadder_1_s1));
  or OR (out_5, halfadder_1_s1, halfadder_2_s1);
  HalfAdder halfadder_2 (.a(halfadder_1_s0), .b(in_3), .s0(out_4), .s1(halfadder_2_s1));
endmodule
