// Logisim project Exemplo0035.circ as structural Verilog: 2 circuits, main circuit Exemplo0035
module Exemplo0035 (
  input  Sinal_a,
  input  a2,
  input  a1,
  input  a0,
  input  Sinal_b,
  input  b2,
  input  b1,
  input  b0,
  output Maior,
  output Igual,
  output Menor
);

  wire comparador_1_s0, comparador_1_s1, comparador_2_s0, comparador_2_s1, comparador_3_s0, comparador_3_s1,
       not_1_out, not_2_out;

  not not_1 (not_1_out, Sinal_a);
  not not_2 (not_2_out, Sinal_b);
  Comparador comparador_1 (
    .c0(1'b0), .c1(1'b1), .a(not_1_out), .b(not_2_out), .s0(comparador_1_s0), .s1(comparador_1_s1));
  Comparador comparador_2 (
    .c0(comparador_3_s0), .c1(comparador_3_s1), .a(a1), .b(b1), .s0(comparador_2_s0), .s1(comparador_2_s1));
  Comparador comparador_3 (
    .c0(comparador_1_s0), .c1(comparador_1_s1), .a(a2), .b(b2), .s0(comparador_3_s0), .s1(comparador_3_s1));
  Comparador comparador_4 (.c0(comparador_2_s0), .c1(comparador_2_s1), .a(a0), .b(b0), .s0(Maior), .s1(Igual));
  xnor xnor_1 (Menor, Igual, Maior);

  // Notes on the sheet:
  //   Exemplo0035
endmodule

// CA
module Comparador (
  input  a,
  input  b,
  input  c0,
  input  c1,
  output s0,
  output s1
);

  wire AND_2_out, AND_3_out, AND_4_out, AND_out, not_1_out, not_2_out;

  not not_1 (not_1_out, b);
  not not_2 (not_2_out, a);
  and AND (AND_out, not_1_out, a, c1);
  and AND_2 (AND_2_out, not_1_out, not_2_out, c1);
  and AND_3 (AND_3_out, b, a, c1);
  and AND_4 (AND_4_out, c0, c1);
  or OR (s0, c0, AND_out);
  or OR_2 (s1, AND_2_out, AND_3_out, AND_4_out);

  // Notes on the sheet:
  //   Comparador
endmodule
