// Logisim project Auxiliar Guia 005.circ as structural Verilog: 3 circuits, main circuit main
module main (
  input  [3:0] a,
  input  [3:0] b
);

  wire and_1_out, and_2_out, maior2bits_1_aviso_do_sinal, maior2bits_1_out_6, not_1_out, not_2_out;

  Maior2Bits maior2bits_1 (
    .a1(a[2]), .a0(a[1]), .b1(b[2]), .b0(b[1]), .Sinal(a[3]), .aviso_do_sinal(maior2bits_1_aviso_do_sinal),
    .out_6(maior2bits_1_out_6));
  not not_1 (not_1_out, b[0]);
  and and_1 (and_1_out, not_1_out, a[0]);
  not not_2 (not_2_out, maior2bits_1_aviso_do_sinal);
  and and_2 (and_2_out, not_2_out, b[3]);
endmodule

module Maior2Bits (
  input  a1,
  input  a0,
  input  Sinal,
  input  b1,
  input  b0,
  output out_6,
  output aviso_do_sinal
);

  wire and_1_out, and_2_out, and_3_out, and_4_out, and_5_out, and_6_out, and_7_out, and_8_out, and_9_out,
       not_1_out, not_2_out, not_3_out, not_4_out, not_5_out, not_6_out, or_1_out, or_2_out, or_3_out,
       xnor_1_out, xnor_2_out;

  not not_1 (not_1_out, Sinal);
  and and_1 (and_1_out, not_1_out, Sinal);
  and and_2 (and_2_out, a1, not_2_out);
  not not_2 (not_2_out, b1);
  xnor xnor_1 (xnor_1_out, Sinal, Sinal);
  not not_3 (not_3_out, Sinal);
  and and_3 (and_3_out, not_3_out, Sinal);
  and and_4 (and_4_out, a0, not_4_out);
  not not_4 (not_4_out, b0);
  xnor xnor_2 (xnor_2_out, Sinal, Sinal);
  and and_5 (and_5_out, and_2_out, xnor_1_out);
  and and_6 (and_6_out, and_4_out, xnor_2_out);
  or or_1 (or_1_out, and_1_out, and_5_out);
  or or_2 (or_2_out, and_3_out, and_6_out);
  and and_7 (and_7_out, b1, a0);
  or or_3 (or_3_out, or_1_out, or_2_out);
  not not_5 (not_5_out, Sinal);
  and and_8 (and_8_out, not_5_out, or_3_out);
  and and_9 (and_9_out, and_8_out, not_6_out);
  not not_6 (not_6_out, and_7_out);
  and and_10 (out_6, and_8_out, and_9_out);

  assign aviso_do_sinal = Sinal;
endmodule

module maior2Bits (
  input  a0,
  input  a1,
  input  a0_2,
  output out_4
);

  wire and_1_out, and_2_out, and_3_out, not_1_out, not_2_out, xnor_1_out;

  not not_1 (not_1_out, a0);
  and and_1 (and_1_out, not_1_out, a0);
  and and_2 (and_2_out, a1, not_2_out);
  not not_2 (not_2_out, a0_2);
  xnor xnor_1 (xnor_1_out, a0, a0);
  and and_3 (and_3_out, and_2_out, xnor_1_out);
  or or_1 (out_4, and_1_out, and_3_out);
endmodule
