// Logisim project Exemplo0032.circ as structural Verilog: 12 circuits, main circuit main
module main (
  input  [3:0] a,
  input  [3:0] b,
  input  Switch,
  output Bit_Desprezivel,
  output [3:0] Saida,
  output out_6
);

  algebrico001 algebrico001_1 (.Carry_Out(Bit_Desprezivel), .a(a), .b(b), .Saida(Saida), .Switch(Switch));
  detectorZero detectorzero_1 (.a3(Saida[0]), .a2(Saida[1]), .a1(Saida[2]), .a0(Saida[3]), .saida(out_6));

  // Notes on the sheet:
  //   Detector de Zeros para 4 Bits
  //   Legenda Switch:
  //   1 - Subtracao
  //   0 - Adicao
endmodule

module fullAdder (
  input  Carry_In,
  input  a,
  input  b,
  output s,
  output Carry_Out
);

  wire A_carry_out, A_saida, B_carry_out;

  or C (Carry_Out, A_carry_out, B_carry_out);
  halfAdder u_A (.Carry_out(A_carry_out), .a(Carry_In), .saida(A_saida), .b(a));
  halfAdder u_B (.Carry_out(B_carry_out), .a(A_saida), .saida(s), .b(b));

  // Notes on the sheet:
  //   Carry Out
  //   s0
  //   s1
  //   saida
  //   c0
endmodule

// H.A.
module halfAdder (
  input  a,
  input  b,
  output Carry_out,
  output saida
);

  and u_A (Carry_out, a, b);
  xor u_B (saida, a, b);
endmodule

module complemento1_4bits (
  input  a0,
  input  a1,
  input  a2,
  input  a3,
  output s0,
  output s1,
  output s2,
  output s3
);

  assign {s3, s2, s1, s0} = ~{a3, a2, a1, a0};  // NOT_Gate not_1, 4 bits wide
endmodule

// COMP2
module complemento2_4bits (
  input  a3,
  input  a2,
  input  a1,
  input  a0,
  output Carry_Out,
  output s3,
  output s2,
  output s1,
  output s0
);

  wire A_carry_out, B_carry_out, complemento1_4bits_1_s0, complemento1_4bits_1_s1, complemento1_4bits_1_s2,
       complemento1_4bits_1_s3, somadorde1_1_carry_out;

  halfAdder C (.Carry_out(Carry_Out), .a(complemento1_4bits_1_s3), .saida(s3), .b(B_carry_out));
  halfAdder B (.Carry_out(B_carry_out), .a(complemento1_4bits_1_s2), .saida(s2), .b(A_carry_out));
  complemento1_4bits complemento1_4bits_1 (
    .a0(a0), .a1(a1), .a2(a2), .a3(a3), .s0(complemento1_4bits_1_s0), .s1(complemento1_4bits_1_s1),
    .s2(complemento1_4bits_1_s2), .s3(complemento1_4bits_1_s3));
  halfAdder A (.Carry_out(A_carry_out), .a(complemento1_4bits_1_s1), .saida(s1), .b(somadorde1_1_carry_out));
  somadorDe1 somadorde1_1 (.Carry_out(somadorde1_1_carry_out), .a(complemento1_4bits_1_s0), .saida(s0));

  // Notes on the sheet:
  //   x3
  //   x2
  //   c2
  //   x1
  //   c1
  //   x0
  //   c0
endmodule

module somadorDe1 (
  input  a,
  output Carry_out,
  output saida
);

  wire C_out, N0_out;

  and u_A (Carry_out, a, C_out);
  xor B (saida, a, C_out);
  not N0 (N0_out, a);
  or C (C_out, N0_out, a);

  // Notes on the sheet:
  //   a
  //   x2
  //   a
  //   x2
  //   x1
  //   a
  //   x2
  //   a
endmodule

// Full Adder 4Bits
module fullAdder_4Bits (
  input  b3,
  input  b2,
  input  b1,
  input  b0,
  input  a3,
  input  a2,
  input  a1,
  input  a0,
  input  Carry_In,
  output Carry_Out,
  output s3,
  output s2,
  output s1,
  output s0
);

  wire fulladder_2_carry_out, fulladder_3_carry_out, fulladder_4_carry_out;

  fullAdder fulladder_1 (.s(s3), .Carry_In(fulladder_2_carry_out), .Carry_Out(Carry_Out), .a(b3), .b(a3));
  fullAdder fulladder_2 (.s(s2), .Carry_In(fulladder_3_carry_out), .Carry_Out(fulladder_2_carry_out), .a(b2), .b(a2));
  fullAdder fulladder_3 (.s(s1), .Carry_In(fulladder_4_carry_out), .Carry_Out(fulladder_3_carry_out), .a(b1), .b(a1));
  fullAdder fulladder_4 (.s(s0), .Carry_In(Carry_In), .Carry_Out(fulladder_4_carry_out), .a(b0), .b(a0));
endmodule

// S.A.
module algebrico001 (
  input  [3:0] a,
  input  [3:0] b,
  input  Switch,
  output Carry_Out,
  output [3:0] Saida
);

  wire A_saida, B_saida, complemento2_4bits_1_carry_out, complemento2_4bits_1_s0, complemento2_4bits_1_s1,
       complemento2_4bits_1_s2, complemento2_4bits_1_s3, fulladder_4bits_1_carry_out, switch_2op_4bits_1_s0,
       switch_2op_4bits_1_s1, switch_2op_4bits_1_s2, switch_2op_4bits_1_s3;

  or C (Carry_Out, A_saida, fulladder_4bits_1_carry_out);
  zerador u_A (.Saida(A_saida), .a(complemento2_4bits_1_carry_out));
  fullAdder_4Bits fulladder_4bits_1 (
    .Carry_Out(fulladder_4bits_1_carry_out), .a3(a[3]), .a2(a[2]), .a1(a[1]), .a0(a[0]),
    .b3(switch_2op_4bits_1_s3), .b2(switch_2op_4bits_1_s2), .b1(switch_2op_4bits_1_s1),
    .b0(switch_2op_4bits_1_s0), .s3(Saida[3]), .s2(Saida[2]), .s1(Saida[1]), .s0(Saida[0]), .Carry_In(B_saida));
  switch_2op_4Bits switch_2op_4bits_1 (
    .a3(b[3]), .a2(b[2]), .a1(b[1]), .a0(b[0]), .a3_prime(complemento2_4bits_1_s3),
    .a2_prime(complemento2_4bits_1_s2), .a1_prime(complemento2_4bits_1_s1),
    .a0_prime(complemento2_4bits_1_s0), .s3(switch_2op_4bits_1_s3), .s2(switch_2op_4bits_1_s2),
    .s1(switch_2op_4bits_1_s1), .s0(switch_2op_4bits_1_s0), .Switch(Switch));
  complemento2_4bits complemento2_4bits_1 (
    .Carry_Out(complemento2_4bits_1_carry_out), .a3(b[3]), .a2(b[2]), .a1(b[1]), .a0(b[0]),
    .s3(complemento2_4bits_1_s3), .s2(complemento2_4bits_1_s2), .s1(complemento2_4bits_1_s1),
    .s0(complemento2_4bits_1_s0));
  zerador u_B (.Saida(B_saida), .a(Switch));
endmodule

// Mux 4Bits
module switch_2op_4Bits (
  input  a3,
  input  a2,
  input  a1,
  input  a0,
  input  a3_prime,
  input  a2_prime,
  input  a1_prime,
  input  a0_prime,
  input  Switch,
  output s3,
  output s2,
  output s1,
  output s0
);

  wire and_1_out, and_2_out, and_3_out, and_4_out, and_5_out, and_6_out, and_7_out, and_8_out, not_1_out,
       not_2_out, not_3_out, not_4_out;

  not not_1 (not_1_out, Switch);
  and and_1 (and_1_out, a3, not_1_out);
  and and_2 (and_2_out, a3_prime, Switch);
  or or_1 (s3, and_1_out, and_2_out);
  not not_2 (not_2_out, Switch);
  and and_3 (and_3_out, a2_prime, Switch);
  and and_4 (and_4_out, a2, not_2_out);
  or or_2 (s2, and_4_out, and_3_out);
  not not_3 (not_3_out, Switch);
  and and_5 (and_5_out, a1_prime, Switch);
  and and_6 (and_6_out, a1, not_3_out);
  or or_3 (s1, and_6_out, and_5_out);
  not not_4 (not_4_out, Switch);
  and and_7 (and_7_out, a0_prime, Switch);
  and and_8 (and_8_out, a0, not_4_out);
  or or_4 (s0, and_8_out, and_7_out);
endmodule

// Zero
module zerador (
  input  a,
  output Saida
);

  wire N_out;

  and u_A (Saida, N_out, a);
  not N (N_out, a);

  // Notes on the sheet:
  //   x0
endmodule

module SomadorAlgebrico4Bits (
  input  [3:0] a,
  input  [3:0] b,
  input  Switch,
  output Bit_Desprezivel,
  output [3:0] Saida
);

  algebrico001 algebrico001_1 (.Carry_Out(Bit_Desprezivel), .a(a), .b(b), .Saida(Saida), .Switch(Switch));

  // Notes on the sheet:
  //   Somador Algebrico de 4 Bits
  //   Legenda Switch:
  //   1 - Subtracao
  //   0 - Adicao
endmodule

// Z.D.
module detectorZero (
  input  a3,
  input  a2,
  input  a1,
  input  a0,
  output saida
);

  wire A_out, B_out, N0_out, N1_out, N2_out, N3_out;

  not N0 (N0_out, a3);
  not N1 (N1_out, a2);
  not N2 (N2_out, a1);
  not N3 (N3_out, a0);
  and A (A_out, N0_out, N1_out);
  and B (B_out, N2_out, N3_out);
  and C (saida, A_out, B_out);

  // Notes on the sheet:
  //   x0
  //   x1
  //   x2
  //   x3
  //   y0
  //   y1
endmodule
