// Logisim project Exemplo0034.circ as structural Verilog
module main (
  input  [3:0] a,
  input  [3:0] b,
  input  Switch,
  output [3:0] Saida,
  output Carry_Out,
  output [3:0] Saida_2,
  output Bit_Desprezivel,
  output [3:0] Saida_3,
  output out_9
);

  algebrico001 algebrico001_1 (
    .Carry_Out(Bit_Desprezivel), .a(a), .b(b), .Saida(Saida_3), .Switch(Switch));  // open: out_5
  FullSubtractor4B fullsubtractor4b_1 (.a(b), .carry_out(Carry_Out), .saida(Saida));
  Incrementador001 incrementador001_1 (
    .a3(b[0]), .a2(b[1]), .a1(b[2]), .a0(b[3]), .s3(Saida_2[3]), .s2(Saida_2[2]), .s1(Saida_2[1]),
    .s0(Saida_2[0]));
  detectorZero detectorzero_1 (.a3(Saida_3[0]), .a2(Saida_3[1]), .a1(Saida_3[2]), .a0(Saida_3[3]), .saida(out_9));

  // Notes on the sheet:
  //   subtrair 1 de B
  //   somar 1 em b
  //   Legenda Switch:
  //   0 - Adicao
  //   Detector de zeros
  //   1 - Subtracao
endmodule

module fullAdder (
  input  Carry_In,
  input  a,
  input  b,
  output s,
  output Carry_Out
);

  wire A_carry_out, A_saida, B_carry_out;

  or C (Carry_Out, A_carry_out, B_carry_out);
  halfAdder u_A (.Carry_out(A_carry_out), .a(Carry_In), .saida(A_saida), .b(a));
  halfAdder u_B (.Carry_out(B_carry_out), .a(A_saida), .saida(s), .b(b));

  // Notes on the sheet:
  //   Carry Out
  //   s0
  //   s1
  //   saida
  //   FULL ADDER
  //   c0
endmodule

// H.A.
module halfAdder (
  input  a,
  input  b,
  output Carry_out,
  output saida
);

  xor u_B (saida, a, b);
  and u_A (Carry_out, a, b);
endmodule

module complemento1_4bits (
  input  a0,
  input  a1,
  input  a2,
  input  a3,
  output s0,
  output s1,
  output s2,
  output s3
);

  assign {s3, s2, s1, s0} = ~{a3, a2, a1, a0};  // NOT_Gate not_1, 4 bits wide

  // Notes on the sheet:
  //   Complemento de 1 para 4 Bits
endmodule

// COMP2
module complemento2_4bits (
  input  a3,
  input  a2,
  input  a1,
  input  a0,
  output Carry_Out,
  output s3,
  output s2,
  output s1,
  output s0
);

  wire A_carry_out, B_carry_out, complemento1_4bits_1_s0, complemento1_4bits_1_s1, complemento1_4bits_1_s2,
       complemento1_4bits_1_s3, somadorde1_1_carry_out;

  halfAdder C (.Carry_out(Carry_Out), .a(complemento1_4bits_1_s3), .saida(s3), .b(B_carry_out));
  halfAdder B (.Carry_out(B_carry_out), .a(complemento1_4bits_1_s2), .saida(s2), .b(A_carry_out));
  complemento1_4bits complemento1_4bits_1 (
    .a0(a0), .a1(a1), .a2(a2), .a3(a3), .s0(complemento1_4bits_1_s0), .s1(complemento1_4bits_1_s1),
    .s2(complemento1_4bits_1_s2), .s3(complemento1_4bits_1_s3));
  halfAdder A (.Carry_out(A_carry_out), .a(complemento1_4bits_1_s1), .saida(s1), .b(somadorde1_1_carry_out));
  somadorDe1 somadorde1_1 (.Carry_out(somadorde1_1_carry_out), .a(complemento1_4bits_1_s0), .saida(s0));

  // Notes on the sheet:
  //   x3
  //   x2
  //   c2
  //   Complemento de 2 para 4 Bits
  //   x1
  //   c1
  //   x0
  //   c0
endmodule

module somadorDe1 (
  input  a,
  output Carry_out,
  output saida
);

  wire C_out, N0_out;

  and u_A (Carry_out, a, C_out);
  xor B (saida, a, C_out);
  not N0 (N0_out, a);
  or C (C_out, N0_out, a);

  // Notes on the sheet:
  //   a
  //   x2
  //   a
  //   Somador de 1 utilizando um Half Adder
  //   x2
  //   x1
  //   a
  //   x2
  //   a
endmodule

// Full Adder 4Bits
module fullAdder_4Bits (
  input  b3,
  input  b2,
  input  b1,
  input  b0,
  input  a3,
  input  a2,
  input  a1,
  input  a0,
  input  Carry_In,
  output Carry_Out,
  output s3,
  output s2,
  output s1,
  output s0,
  output out_15,
  output out_16,
  output out_17
);

  fullAdder fulladder_1 (.s(s3), .Carry_In(out_15), .Carry_Out(Carry_Out), .a(b3), .b(a3));
  fullAdder fulladder_2 (.s(s2), .Carry_In(out_16), .Carry_Out(out_15), .a(b2), .b(a2));
  fullAdder fulladder_3 (.s(s1), .Carry_In(out_17), .Carry_Out(out_16), .a(b1), .b(a1));
  fullAdder fulladder_4 (.s(s0), .Carry_In(Carry_In), .Carry_Out(out_17), .a(b0), .b(a0));

  // Notes on the sheet:
  //   Full Adder para 4 Bits
endmodule

// S.A.
module algebrico001 (
  input  [3:0] a,
  input  [3:0] b,
  input  Switch,
  output Carry_Out,
  output [2:0] out_5,
  output [3:0] Saida
);

  wire A_saida, B_saida, complemento2_4bits_1_carry_out, complemento2_4bits_1_s0, complemento2_4bits_1_s1,
       complemento2_4bits_1_s2, complemento2_4bits_1_s3, fulladder_4bits_1_carry_out, switch_2op_4bits_1_s0,
       switch_2op_4bits_1_s1, switch_2op_4bits_1_s2, switch_2op_4bits_1_s3;

  or C (Carry_Out, A_saida, fulladder_4bits_1_carry_out);
  zerador u_A (.Saida(A_saida), .a(complemento2_4bits_1_carry_out));
  fullAdder_4Bits fulladder_4bits_1 (
    .Carry_Out(fulladder_4bits_1_carry_out), .out_15(out_5[0]), .out_16(out_5[1]), .out_17(out_5[2]),
    .a3(a[3]), .a2(a[2]), .a1(a[1]), .a0(a[0]), .b3(switch_2op_4bits_1_s3), .b2(switch_2op_4bits_1_s2),
    .b1(switch_2op_4bits_1_s1), .b0(switch_2op_4bits_1_s0), .s3(Saida[3]), .s2(Saida[2]), .s1(Saida[1]),
    .s0(Saida[0]), .Carry_In(B_saida));
  switch_2op_4Bits switch_2op_4bits_1 (
    .a3(b[3]), .a2(b[2]), .a1(b[1]), .a0(b[0]), .a3_prime(complemento2_4bits_1_s3),
    .a2_prime(complemento2_4bits_1_s2), .a1_prime(complemento2_4bits_1_s1),
    .a0_prime(complemento2_4bits_1_s0), .s3(switch_2op_4bits_1_s3), .s2(switch_2op_4bits_1_s2),
    .s1(switch_2op_4bits_1_s1), .s0(switch_2op_4bits_1_s0), .Switch(Switch));
  complemento2_4bits complemento2_4bits_1 (
    .Carry_Out(complemento2_4bits_1_carry_out), .a3(b[3]), .a2(b[2]), .a1(b[1]), .a0(b[0]),
    .s3(complemento2_4bits_1_s3), .s2(complemento2_4bits_1_s2), .s1(complemento2_4bits_1_s1),
    .s0(complemento2_4bits_1_s0));
  zerador u_B (.Saida(B_saida), .a(Switch));

  // Notes on the sheet:
  //   Somador Algebrico de 4 Bits
endmodule

// Mux 4Bits
module switch_2op_4Bits (
  input  a3,
  input  a2,
  input  a1,
  input  a0,
  input  a3_prime,
  input  a2_prime,
  input  a1_prime,
  input  a0_prime,
  input  Switch,
  output s3,
  output s2,
  output s1,
  output s0
);

  wire and_1_out, and_2_out, and_3_out, and_4_out, and_5_out, and_6_out, and_7_out, and_8_out, not_1_out,
       not_2_out, not_3_out, not_4_out;

  not not_1 (not_1_out, Switch);
  and and_1 (and_1_out, a3, not_1_out);
  and and_2 (and_2_out, a3_prime, Switch);
  or or_1 (s3, and_1_out, and_2_out);
  not not_2 (not_2_out, Switch);
  and and_3 (and_3_out, a2, not_2_out);
  and and_4 (and_4_out, a2_prime, Switch);
  or or_2 (s2, and_3_out, and_4_out);
  not not_3 (not_3_out, Switch);
  and and_5 (and_5_out, a1, not_3_out);
  and and_6 (and_6_out, a1_prime, Switch);
  or or_3 (s1, and_5_out, and_6_out);
  not not_4 (not_4_out, Switch);
  and and_7 (and_7_out, a0_prime, Switch);
  and and_8 (and_8_out, a0, not_4_out);
  or or_4 (s0, and_8_out, and_7_out);

  // Notes on the sheet:
  //   Switch de 2 opções para 4 Bits
endmodule

// Zero
module zerador (
  input  a,
  output Saida
);

  wire N_out;

  and u_A (Saida, N_out, a);
  not N (N_out, a);

  // Notes on the sheet:
  //   Mantem uma saida com Bit zero independente da entrada
  //   x0
endmodule

module SomadorAlgebrico4Bits (
  input  [3:0] a,
  input  [3:0] b,
  input  Switch,
  output Bit_Desprezivel,
  output [3:0] Saida
);

  algebrico001 algebrico001_1 (
    .Carry_Out(Bit_Desprezivel), .a(a), .b(b), .Saida(Saida), .Switch(Switch));  // open: out_5

  // Notes on the sheet:
  //   Somador Algebrico de 4 Bits
  //   Legenda Switch:
  //   1 - Subtracao
  //   0 - Adicao
endmodule

// Z.D.
module detectorZero (
  input  a3,
  input  a2,
  input  a1,
  input  a0,
  output saida
);

  wire N0_out, N1_out, N2_out, N3_out;

  not N0 (N0_out, a3);
  not N1 (N1_out, a2);
  not N2 (N2_out, a1);
  not N3 (N3_out, a0);
  and A (saida, N0_out, N1_out, N2_out, N3_out);

  // Notes on the sheet:
  //   Detecta se a saida e igual a zero
  //   x0
  //   x1
  //   x2
  //   x3
endmodule

module Exemplo0032 (
  input  [3:0] a,
  input  [3:0] b,
  input  Switch,
  output Bit_Desprezivel,
  output [3:0] Saida,
  output out_6
);

  algebrico001 algebrico001_1 (
    .Carry_Out(Bit_Desprezivel), .a(a), .b(b), .Saida(Saida), .Switch(Switch));  // open: out_5
  detectorZero detectorzero_1 (.a3(Saida[0]), .a2(Saida[1]), .a1(Saida[2]), .a0(Saida[3]), .saida(out_6));

  // Notes on the sheet:
  //   Detector de Zeros para 4 Bits
  //   Legenda Switch:
  //   1 - Subtracao
  //   0 - Adicao
  //   Detector de zeros
endmodule

module incrementador (
  input  a,
  input  b,
  input  c,
  input  d,
  output s3,
  output s2,
  output s1,
  output s0
);

  wire and_1_out, and_2_out, and_3_out, and_4_out, and_5_out, and_6_out, and_7_out, and_8_out, not_1_out,
       not_2_out, not_3_out, not_4_out, not_5_out, not_6_out, or_1_out, or_2_out, or_3_out, or_4_out,
       xnor_1_out, xnor_2_out, xor_1_out, xor_2_out, xor_3_out, xor_4_out, xor_5_out, xor_6_out;

  not not_1 (not_1_out, b);
  and and_1 (and_1_out, not_1_out, not_2_out);
  not not_2 (not_2_out, c);
  xor xor_1 (xor_1_out, b, c);
  and and_2 (and_2_out, b, c);
  xor xor_2 (xor_2_out, a, d);
  not not_3 (not_3_out, c);
  and and_3 (and_3_out, not_3_out, not_4_out);
  not not_4 (not_4_out, d);
  xor xor_3 (xor_3_out, c, d);
  not not_5 (not_5_out, b);
  and and_4 (and_4_out, c, d);
  xor xor_4 (xor_4_out, c, d);
  xor xor_5 (xor_5_out, a, b);
  not not_6 (not_6_out, d);
  xor xor_6 (xor_6_out, a, b);
  and and_5 (and_5_out, a, or_1_out);
  or or_1 (or_1_out, and_1_out, xor_1_out);
  and and_6 (and_6_out, and_2_out, xor_2_out);
  or or_2 (or_2_out, and_3_out, xor_3_out);
  or or_3 (or_3_out, xor_5_out, xnor_1_out);
  xnor xnor_1 (xnor_1_out, a, b);
  xnor xnor_2 (xnor_2_out, a, b);
  or or_4 (or_4_out, xnor_2_out, xor_6_out);
  and and_7 (and_7_out, b, or_2_out);
  and and_8 (and_8_out, not_5_out, and_4_out);
  and and_9 (s1, xor_4_out, or_3_out);
  and and_10 (s0, not_6_out, or_4_out);
  or or_5 (s3, and_5_out, and_6_out);
  or or_6 (s2, and_7_out, and_8_out);
endmodule

// Cont
module Incrementador001 (
  input  a3,
  input  a2,
  input  a1,
  input  a0,
  output s3,
  output s2,
  output s1,
  output s0
);

  wire A_out, B_out, C_out, D_out, E_out, F_out, G_out, H_out, I_out, J_out, K_out, L_out, M_out, N0_out,
       N1_out, N2_out, N3_out, N4_out, N5_out, N_out, O_out, P_out;

  not N0 (N0_out, a1);
  and A (A_out, N0_out, N1_out);
  not N1 (N1_out, a2);
  and C (C_out, a1, a2);
  not N2 (N2_out, a2);
  and E (E_out, N2_out, N3_out);
  not N3 (N3_out, a3);
  not N4 (N4_out, a1);
  and G (G_out, a2, a3);
  not N5 (N5_out, a3);
  or J (J_out, A_out, B_out);
  xor B (B_out, a1, a2);
  and K (K_out, C_out, D_out);
  xor D (D_out, a0, a3);
  or L (L_out, E_out, F_out);
  xor F (F_out, a2, a3);
  xor H (H_out, a0, a1);
  or M (M_out, H_out, I_out);
  xnor I (I_out, a0, a1);
  and N (N_out, a0, J_out);
  and O (O_out, a1, L_out);
  and P (P_out, N4_out, G_out);
  or Q (s3, N_out, K_out);
  or R (s2, O_out, P_out);
  and S (s1, F_out, M_out);
  and T (s0, M_out, N5_out);

  // Notes on the sheet:
  //   a1
  //   a2
  //   a2
  //   a3
  //   a1
  //   x0
  //   x1
  //   a1
  //   a2
  //   a1
  //   a2
  //   a0
  //   a3
  //   x2
  //   x3
  //   a2
  //   a3
  //   a2
  //   a3
  //   a0
  //   a1
  //   a0
  //   a1
  //   a3
  //   w0
  //   y0
  //   y1
  //   y2
  //   y3
  //   y4
  //   y5
  //   y7
  //   y8
  //   a0
  //   z0
  //   w1
  //   a1
  //   w2
  //   z1
  //   z2
  //   x4
  //   y6
  //   y5
  //   w3
  //   w3
  //   x5
endmodule

module HalfSubtractor (
  input  Carry_In,
  input  a,
  output saida,
  output Carry_Out
);

  wire N1_out;

  xor u_A (saida, Carry_In, a);
  not N1 (N1_out, a);
  and B (Carry_Out, N1_out, Carry_In);
endmodule

module FullSubtractor (
  input  Carry_In,
  input  a,
  input  b,
  output Saida,
  output Carry_Out
);

  wire halfsubtractor_1_carry_out, halfsubtractor_1_saida, halfsubtractor_2_carry_out;

  HalfSubtractor halfsubtractor_1 (
    .a(a), .Carry_In(b), .Carry_Out(halfsubtractor_1_carry_out), .saida(halfsubtractor_1_saida));
  HalfSubtractor halfsubtractor_2 (
    .a(halfsubtractor_1_saida), .Carry_In(Carry_In), .Carry_Out(halfsubtractor_2_carry_out), .saida(Saida));
  or E (Carry_Out, halfsubtractor_2_carry_out, halfsubtractor_1_carry_out);
endmodule

module FullSubtractor4B (
  input  [3:0] a,
  output [3:0] saida,
  output carry_out
);

  wire A_out, fullsubtractor_1_carry_out, fullsubtractor_2_carry_out, fullsubtractor_3_carry_out, N_out,
       zerador_1_saida, zerador_2_saida, zerador_3_saida, zerador_4_saida;

  not N (N_out, a[0]);
  zerador zerador_1 (.Saida(zerador_1_saida), .a(a[0]));
  zerador zerador_2 (.Saida(zerador_2_saida), .a(a[1]));
  zerador zerador_3 (.Saida(zerador_3_saida), .a(a[2]));
  zerador zerador_4 (.Saida(zerador_4_saida), .a(a[3]));
  or u_A (A_out, N_out, a[0]);
  FullSubtractor fullsubtractor_1 (
    .a(a[0]), .b(zerador_1_saida), .Carry_In(A_out), .Carry_Out(fullsubtractor_1_carry_out), .Saida(saida[0]));
  FullSubtractor fullsubtractor_2 (
    .a(a[1]), .b(zerador_2_saida), .Carry_In(fullsubtractor_1_carry_out),
    .Carry_Out(fullsubtractor_2_carry_out), .Saida(saida[1]));
  FullSubtractor fullsubtractor_3 (
    .a(a[2]), .b(zerador_3_saida), .Carry_In(fullsubtractor_2_carry_out),
    .Carry_Out(fullsubtractor_3_carry_out), .Saida(saida[2]));
  FullSubtractor fullsubtractor_4 (
    .a(a[3]), .b(zerador_4_saida), .Carry_In(fullsubtractor_3_carry_out), .Carry_Out(carry_out),
    .Saida(saida[3]));

  // Notes on the sheet:
  //   a0
  //   n1
  //   a0
  //   w
  //   w
  //   y0
  //   x1
  //   y1
  //   x2
  //   y2
  //   x3
  //   y3
endmodule
