// Logisim project Exemplo0035.circ as structural Verilog
module Maior (
  input  sinal_de_a,
  input  a,
  input  sinal_de_b,
  input  b,
  output out_5
);

  wire and_1_out, and_2_out, and_3_out, and_4_out, and_5_out, and_6_out, not_1_out, not_2_out, not_3_out,
       or_1_out, xnor_1_out, xnor_2_out, xor_1_out;

  not not_1 (not_1_out, b);
  not not_2 (not_2_out, sinal_de_a);
  not not_3 (not_3_out, sinal_de_a);
  xnor xnor_1 (xnor_1_out, sinal_de_a, a);
  and and_1 (and_1_out, sinal_de_b, not_1_out);
  xor xor_1 (xor_1_out, a, b);
  and and_2 (and_2_out, not_2_out, sinal_de_b);
  xnor xnor_2 (xnor_2_out, sinal_de_b, b);
  and and_3 (and_3_out, not_3_out, a);
  and and_4 (and_4_out, xnor_1_out, and_1_out);
  and and_5 (and_5_out, xor_1_out, and_2_out);
  and and_6 (and_6_out, xnor_2_out, and_3_out);
  or or_1 (or_1_out, and_4_out, and_5_out);
  or or_2 (out_5, or_1_out, and_6_out);
endmodule

module Menor (
  input  a1,
  input  a0,
  input  b1,
  input  b0,
  output out_5
);

  wire A_out, B_out, C_out, D_out, E_out, F_out, G_out, H_out, I_out, J_out, N0_out, N1_out, N2_out;

  not N0 (N0_out, a1);
  not N1 (N1_out, a0);
  xor A (A_out, b1, b0);
  not N2 (N2_out, a1);
  xor B (B_out, a0, b0);
  xor C (C_out, a1, a0);
  and D (D_out, N0_out, N1_out);
  and E (E_out, N2_out, b1);
  and F (F_out, b1, b0);
  and G (G_out, D_out, A_out);
  or J (J_out, G_out, H_out);
  and H (H_out, E_out, B_out);
  and I (I_out, F_out, C_out);
  or K (out_5, J_out, I_out);

  // Notes on the sheet:
  //   n0
  //   n1
  //   n2
  //   x3
  //   x0
  //   x4
  //   x1
  //   x5
  //   x2
  //   x6
  //   x7
  //   x9
  //   x8
endmodule

module Igual (
  input  a1,
  input  a0,
  input  b1,
  input  b0,
  output Saida
);

  wire A_out, B_out;

  xnor A (A_out, a0, b0);
  xnor B (B_out, a1, b1);
  and C (Saida, A_out, B_out);

  // Notes on the sheet:
  //   x0
  //   x1
endmodule

module Maior4Bits (
  input  [3:0] a,
  input  [3:0] b
);

  wire maior_1_out_5, maior_2_out_5, or_1_out;

  LED led_1 (.in(or_1_out));
  Maior maior_1 (.sinal_de_a(a[3]), .sinal_de_b(b[3]), .out_5(maior_1_out_5));  // open: a, b
  Maior maior_2 (.out_5(maior_2_out_5));  // open: sinal_de_a, a, sinal_de_b, b
  or or_1 (or_1_out, maior_1_out_5, maior_2_out_5);
endmodule

module Maior002 (
);

  wire and_1_out, and_2_out, and_3_out, and_5_out, not_1_out, not_2_out, not_3_out, xnor_1_out, xnor_2_out,
       xor_1_out;

  // NOT_Gate not_1 has open pins: in=open, out=not_1_out
  // NOT_Gate not_2 has open pins: in=open, out=not_2_out
  // NOT_Gate not_3 has open pins: in=open, out=not_3_out
  // XNOR_Gate xnor_1 has open pins: out=xnor_1_out
  buf and_1 (and_1_out, not_1_out);  // AND_Gate
  // XOR_Gate xor_1 has open pins: out=xor_1_out
  buf and_2 (and_2_out, not_2_out);  // AND_Gate
  // XNOR_Gate xnor_2 has open pins: out=xnor_2_out
  buf and_3 (and_3_out, not_3_out);  // AND_Gate
  // AND_Gate and_4 has open pins: in0=xnor_1_out, in1=and_1_out, out=open
  and and_5 (and_5_out, xor_1_out, and_2_out);
  // AND_Gate and_6 has open pins: in0=xnor_2_out, in1=and_3_out, out=open
endmodule
