// Logisim project Guia05Exemplo0035.circ as structural Verilog: 2 circuits, main circuit main
module main (
  input  a2,
  input  a1,
  input  a0,
  input  Sinal_b,
  input  Sinal_a,
  input  b2,
  input  b1,
  input  b0,
  output Maior,
  output Igual,
  output Menor
);

  wire ca_1_s0, ca_1_s1, ca_2_s0, ca_2_s1, ca_3_s0, ca_3_s1, not_1_out, not_2_out;

  not not_1 (not_1_out, Sinal_a);
  not not_2 (not_2_out, Sinal_b);
  ca ca_1 (.c0(1'b0), .c1(1'b1), .a(not_1_out), .b(not_2_out), .s0(ca_1_s0), .s1(ca_1_s1));
  ca ca_2 (.c0(ca_3_s0), .c1(ca_3_s1), .a(a1), .b(b1), .s0(ca_2_s0), .s1(ca_2_s1));
  ca ca_3 (.c0(ca_1_s0), .c1(ca_1_s1), .a(a2), .b(b2), .s0(ca_3_s0), .s1(ca_3_s1));
  ca ca_4 (.c0(ca_2_s0), .c1(ca_2_s1), .a(a0), .b(b0), .s0(Maior), .s1(Igual));
  xnor xnor_1 (Menor, Igual, Maior);
endmodule

module ca (
  input  a,
  input  b,
  input  c0,
  input  c1,
  output s0,
  output s1
);

  wire and_1_out, and_2_out, and_3_out, and_4_out, not_1_out, not_2_out;

  not not_1 (not_1_out, b);
  not not_2 (not_2_out, a);
  or or_1 (s0, c0, and_1_out);
  and and_1 (and_1_out, not_1_out, a, c1);
  and and_2 (and_2_out, not_1_out, not_2_out, c1);
  or or_2 (s1, and_2_out, and_3_out, and_4_out);
  and and_3 (and_3_out, b, a, c1);
  and and_4 (and_4_out, c0, c1);
endmodule
