// Logisim project Exemplo0034.circ as structural Verilog: 3 circuits, main circuit main
module main (
  input  in_1,
  input  in_2,
  input  in_3,
  input  in_4,
  input  in_5,
  input  in_6,
  input  in_7,
  input  in_8,
  input  in_9,
  output out_10,
  output out_11,
  output out_12,
  output out_13,
  output out_14,
  output out_15
);

  wire fulladder_1_out_5, fulladder_2_out_5, fulladder_3_out_5, fulladder_4_out_5, not_1_out, xor_2_out,
       xor_3_out, xor_4_out, xor_5_out;

  xor xor_1 (out_10, in_9, fulladder_1_out_5);
  xor xor_2 (xor_2_out, in_2, in_9);
  FullAdder fulladder_1 (
    .out_5(fulladder_1_out_5), .in_1(in_1), .in_2(xor_2_out), .out_4(out_11), .in_3(fulladder_2_out_5));
  xor xor_3 (xor_3_out, in_4, in_9);
  FullAdder fulladder_2 (
    .out_5(fulladder_2_out_5), .in_1(in_3), .in_2(xor_3_out), .out_4(out_12), .in_3(fulladder_3_out_5));
  xor xor_4 (xor_4_out, in_6, in_9);
  FullAdder fulladder_3 (
    .out_5(fulladder_3_out_5), .in_1(in_5), .in_2(xor_4_out), .out_4(out_13), .in_3(fulladder_4_out_5));
  xor xor_5 (xor_5_out, in_8, in_9);
  FullAdder fulladder_4 (.out_5(fulladder_4_out_5), .in_1(in_7), .in_2(xor_5_out), .out_4(out_14), .in_3(not_1_out));
  not not_1 (not_1_out, 1'b1);
  nor nor_1 (out_15, out_10, out_11, out_12, out_13, out_14);
endmodule

// HA
module HalfAdder (
  input  a,
  input  b,
  output s0,
  output s1
);

  xor xor_1 (s0, a, b);
  and and_1 (s1, a, b);
endmodule

// FA
module FullAdder (
  input  in_1,
  input  in_2,
  input  in_3,
  output out_4,
  output out_5
);

  wire halfadder_1_s0, halfadder_1_s1, halfadder_2_s1;

  HalfAdder halfadder_1 (.a(in_1), .b(in_2), .s0(halfadder_1_s0), .s1(halfadder_1_s1));
  or or_1 (out_5, halfadder_1_s1, halfadder_2_s1);
  HalfAdder halfadder_2 (.a(halfadder_1_s0), .b(in_3), .s0(out_4), .s1(halfadder_2_s1));
endmodule
