// Logisim project Exercicio05.circ as structural Verilog: 1 circuit, main circuit main
module main (
  input  CLK,
  input  in_2,
  input  CLR,
  input  LD,
  input  d4,
  input  d3,
  input  d2,
  input  d1,
  input  d0,
  output a,
  output b,
  output c,
  output d,
  output e
);

  wire And01_out, And02_out, And03_out, And04_out, And05_out;

  D_Flip_Flop d_ff_1 (.clk(CLK), .D(in_2), .Q(a), .preset(And01_out), .reset(CLR));  // open: Qn, en
  and And01 (And01_out, LD, d4);
  D_Flip_Flop d_ff_2 (.clk(CLK), .D(a), .Q(b), .preset(And02_out), .reset(CLR));  // open: Qn, en
  and And02 (And02_out, LD, d3);
  D_Flip_Flop d_ff_3 (.clk(CLK), .D(b), .Q(c), .preset(And03_out), .reset(CLR));  // open: Qn, en
  and And03 (And03_out, LD, d2);
  D_Flip_Flop d_ff_4 (.clk(CLK), .D(c), .Q(d), .preset(And04_out), .reset(CLR));  // open: Qn, en
  and And04 (And04_out, LD, d1);
  D_Flip_Flop d_ff_5 (.clk(CLK), .D(d), .Q(e), .preset(And05_out), .reset(CLR));  // open: Qn, en
  and And05 (And05_out, LD, d0);
endmodule
