// Logisim project Circuitos.circ as structural Verilog: 5 circuits, main circuit Exemplo0052
module Exemplo0052 (
  input  DATA,
  input  RST,
  output out_3
);

  wire CLK_out, d_ff_1_q, d_ff_2_q, d_ff_3_q, d_ff_4_q, not_1_out, not_2_out;

  Clock CLK (.out(CLK_out));
  D_Flip_Flop d_ff_1 (.clk(CLK_out), .D(DATA), .Q(d_ff_1_q), .reset(RST));  // open: Qn, preset, en
  D_Flip_Flop d_ff_2 (.clk(CLK_out), .D(d_ff_1_q), .Q(d_ff_2_q), .reset(RST));  // open: Qn, preset, en
  D_Flip_Flop d_ff_3 (.clk(CLK_out), .D(d_ff_2_q), .Q(d_ff_3_q), .reset(RST));  // open: Qn, preset, en
  D_Flip_Flop d_ff_4 (.clk(CLK_out), .D(d_ff_3_q), .Q(d_ff_4_q), .reset(RST));  // open: Qn, preset, en
  not not_1 (not_1_out, d_ff_3_q);
  and and_1 (out_3, d_ff_4_q, not_1_out, not_2_out, d_ff_1_q);
  not not_2 (not_2_out, d_ff_2_q);

  // Notes on the sheet:
  //   396679 - Bruno Cezar Andrade Viallet - Mealy1001
endmodule

module Exemplo0053 (
  input  in_1,
  input  RST,
  output out_3
);

  wire and_1_out, CLK_out, d_ff_1_q, d_ff_2_q, d_ff_3_q, d_ff_4_q, not_1_out, not_2_out;

  Clock CLK (.out(CLK_out));
  D_Flip_Flop d_ff_1 (.clk(CLK_out), .D(in_1), .Q(d_ff_1_q), .reset(RST));  // open: Qn, preset, en
  D_Flip_Flop d_ff_2 (.clk(CLK_out), .D(d_ff_1_q), .Q(d_ff_2_q), .reset(RST));  // open: Qn, preset, en
  D_Flip_Flop d_ff_3 (.clk(CLK_out), .D(d_ff_2_q), .Q(d_ff_3_q), .reset(RST));  // open: Qn, preset, en
  D_Flip_Flop d_ff_4 (.clk(CLK_out), .D(d_ff_3_q), .Q(d_ff_4_q), .reset(RST));  // open: Qn, preset, en
  D_Flip_Flop d_ff_5 (.clk(CLK_out), .D(and_1_out), .Q(out_3), .reset(RST));  // open: Qn, preset, en
  not not_1 (not_1_out, d_ff_3_q);
  and and_1 (and_1_out, d_ff_4_q, not_1_out, not_2_out, d_ff_1_q);
  not not_2 (not_2_out, d_ff_2_q);

  // Notes on the sheet:
  //   396679 - Bruno Cezar Andrade Viallet - Moore1001
endmodule

module Exemplo0054 (
  input  DATA,
  input  RST,
  output out_3
);

  wire CLK_out, d_ff_1_q, d_ff_2_q, d_ff_3_q, d_ff_4_q, not_1_out;

  Clock CLK (.out(CLK_out));
  D_Flip_Flop d_ff_1 (.clk(CLK_out), .D(DATA), .Q(d_ff_1_q), .reset(RST));  // open: Qn, preset, en
  D_Flip_Flop d_ff_2 (.clk(CLK_out), .D(d_ff_1_q), .Q(d_ff_2_q), .reset(RST));  // open: Qn, preset, en
  D_Flip_Flop d_ff_3 (.clk(CLK_out), .D(d_ff_2_q), .Q(d_ff_3_q), .reset(RST));  // open: Qn, preset, en
  D_Flip_Flop d_ff_4 (.clk(CLK_out), .D(d_ff_3_q), .Q(d_ff_4_q), .reset(RST));  // open: Qn, preset, en
  not not_1 (not_1_out, d_ff_4_q);
  and and_1 (out_3, not_1_out, d_ff_3_q, d_ff_2_q, d_ff_1_q);

  // Notes on the sheet:
  //   396679 - Bruno Cezar Andrade Viallet - Mealy1110
endmodule

module Exemplo0055 (
  input  in_1,
  input  RST,
  output out_3
);

  wire CLK_out, d_ff_1_q, d_ff_2_q, d_ff_3_q, d_ff_4_q, not_1_out, not_2_out, not_3_out, not_4_out, or_1_out;

  Clock CLK (.out(CLK_out));
  D_Flip_Flop d_ff_1 (.clk(CLK_out), .D(in_1), .Q(d_ff_1_q), .reset(RST));  // open: Qn, preset, en
  D_Flip_Flop d_ff_2 (.clk(CLK_out), .D(d_ff_1_q), .Q(d_ff_2_q), .reset(RST));  // open: Qn, preset, en
  D_Flip_Flop d_ff_3 (.clk(CLK_out), .D(d_ff_2_q), .Q(d_ff_3_q), .reset(RST));  // open: Qn, preset, en
  D_Flip_Flop d_ff_4 (.clk(CLK_out), .D(d_ff_3_q), .Q(d_ff_4_q), .reset(RST));  // open: Qn, preset, en
  not not_1 (not_1_out, d_ff_1_q);
  not not_2 (not_2_out, d_ff_4_q);
  not not_3 (not_3_out, d_ff_3_q);
  and and_1 (out_3, not_2_out, not_3_out, not_4_out, or_1_out);
  not not_4 (not_4_out, d_ff_2_q);
  or or_1 (or_1_out, d_ff_1_q, not_1_out);

  // Notes on the sheet:
  //   396679 - Bruno Cezar Andrade Viallet - Mealy x000
endmodule

module Exemplo0056 (
  input  DATA,
  input  RST,
  output out_3
);

  wire and_1_out, and_2_out, CLK_out, d_ff_1_q, d_ff_2_q, d_ff_3_q;

  Clock CLK (.out(CLK_out));
  D_Flip_Flop d_ff_1 (.clk(CLK_out), .D(DATA), .Q(d_ff_1_q), .reset(RST));  // open: Qn, preset, en
  D_Flip_Flop d_ff_2 (.clk(CLK_out), .D(d_ff_1_q), .Q(d_ff_2_q), .reset(RST));  // open: Qn, preset, en
  D_Flip_Flop d_ff_3 (.clk(CLK_out), .D(d_ff_2_q), .Q(d_ff_3_q), .reset(RST));  // open: Qn, preset, en
  and and_1 (and_1_out, d_ff_3_q, d_ff_2_q, d_ff_1_q);
  and and_2 (and_2_out, ~d_ff_3_q, ~d_ff_2_q, ~d_ff_1_q);  // AND_Gate
  or or_1 (out_3, and_1_out, and_2_out);

  // Notes on the sheet:
  //   396679 - Bruno Cezar Andrade Viallet - Mealy000 ou 111
endmodule
