// Logisim project Exemplo0052.circ as structural Verilog: 1 circuit, main circuit main
module main (
  input  entrada,
  output saida
);

  wire _00_q, _01_q, _01_qn, _10_q, _10_qn, _11_q, clk_out;

  Clock clk (.out(clk_out));
  D_Flip_Flop _00 (.clk(clk_out), .D(entrada), .Q(_00_q));  // open: Qn, preset, en, reset
  D_Flip_Flop _01 (.clk(clk_out), .D(_00_q), .Q(_01_q), .Qn(_01_qn));  // open: preset, en, reset
  D_Flip_Flop _10 (.clk(clk_out), .D(_01_q), .Q(_10_q), .Qn(_10_qn));  // open: preset, en, reset
  D_Flip_Flop _11 (.clk(clk_out), .D(_10_q), .Q(_11_q));  // open: Qn, preset, en, reset
  and and_1 (saida, _11_q, _10_qn, _01_qn, _00_q);
endmodule
