// Logisim project Exemplo0054.circ as structural Verilog: 1 circuit, main circuit main
module main (
  input  e,
  output s
);

  wire _00_q, _01_q, _10_q, _11_qn, clk_out;

  Clock clk (.out(clk_out));
  D_Flip_Flop _00 (.clk(clk_out), .D(e), .Q(_00_q));  // open: Qn, preset, en, reset
  D_Flip_Flop _01 (.clk(clk_out), .D(_00_q), .Q(_01_q));  // open: Qn, preset, en, reset
  D_Flip_Flop _10 (.clk(clk_out), .D(_01_q), .Q(_10_q));  // open: Qn, preset, en, reset
  D_Flip_Flop _11 (.clk(clk_out), .D(_10_q), .Qn(_11_qn));  // open: Q, preset, en, reset
  and and_1 (s, _00_q, _01_q, _10_q, _11_qn);
endmodule
