// Logisim project Guia 07.circ as structural Verilog
module Exemplo0052 (
  input  I,
  output S
);

  wire clk_out, d_ff_1_q, d_ff_2_q, d_ff_2_qn, d_ff_3_q;

  Clock clk (.out(clk_out));
  D_Flip_Flop d_ff_1 (.clk(clk_out), .D(I), .Q(d_ff_1_q));  // open: Qn, preset, en, reset
  D_Flip_Flop d_ff_2 (.clk(clk_out), .D(d_ff_1_q), .Q(d_ff_2_q), .Qn(d_ff_2_qn));  // open: preset, en, reset
  D_Flip_Flop d_ff_3 (.clk(clk_out), .D(d_ff_2_q), .Q(d_ff_3_q));  // open: Qn, preset, en, reset
  and and_1 (S, d_ff_3_q, d_ff_2_qn, d_ff_1_q);

  // Notes on the sheet:
  //   João Henrique - 392734
endmodule

module Exemplo0053 (
  input  I,
  output S
);

  wire and_1_out, clk_out, d_ff_1_q, d_ff_1_qn, d_ff_2_q, d_ff_3_q, d_ff_3_qn, d_ff_4_q;

  Clock clk (.out(clk_out));
  D_Flip_Flop d_ff_1 (.clk(clk_out), .D(I), .Q(d_ff_1_q), .Qn(d_ff_1_qn), .reset(S));  // open: preset, en
  D_Flip_Flop d_ff_2 (.clk(clk_out), .D(d_ff_1_q), .Q(d_ff_2_q), .reset(S));  // open: Qn, preset, en
  D_Flip_Flop d_ff_3 (.clk(clk_out), .D(d_ff_2_q), .Q(d_ff_3_q), .Qn(d_ff_3_qn), .reset(S));  // open: preset, en
  D_Flip_Flop d_ff_4 (.clk(clk_out), .D(d_ff_3_q), .Q(d_ff_4_q), .reset(S));  // open: Qn, preset, en
  and and_1 (and_1_out, d_ff_4_q, d_ff_3_qn, d_ff_2_q, d_ff_1_qn);
  D_Flip_Flop d_ff_5 (.clk(clk_out), .D(and_1_out), .Q(S));  // open: Qn, preset, en, reset

  // Notes on the sheet:
  //   João Henrique - 392734
endmodule

module Exemplo0054 (
  input  I,
  output S
);

  wire clk_out, d_ff_1_q, d_ff_2_q, d_ff_3_q, d_ff_4_qn;

  Clock clk (.out(clk_out));
  D_Flip_Flop d_ff_1 (.clk(clk_out), .D(I), .Q(d_ff_1_q));  // open: Qn, preset, en, reset
  D_Flip_Flop d_ff_2 (.clk(clk_out), .D(d_ff_1_q), .Q(d_ff_2_q));  // open: Qn, preset, en, reset
  D_Flip_Flop d_ff_3 (.clk(clk_out), .D(d_ff_2_q), .Q(d_ff_3_q));  // open: Qn, preset, en, reset
  D_Flip_Flop d_ff_4 (.clk(clk_out), .D(d_ff_3_q), .Qn(d_ff_4_qn));  // open: Q, preset, en, reset
  and and_1 (S, d_ff_4_qn, d_ff_3_q, d_ff_2_q, d_ff_1_q);

  // Notes on the sheet:
  //   João Henrique - 392734
endmodule

module Exemplo0055 (
  input  I,
  output S
);

  wire clk_out, d_ff_1_q, d_ff_2_q, d_ff_3_q, d_ff_4_q, d_ff_4_qn, or_1_out;

  Clock clk (.out(clk_out));
  D_Flip_Flop d_ff_1 (.clk(clk_out), .D(I), .Q(d_ff_1_q));  // open: Qn, preset, en, reset
  D_Flip_Flop d_ff_2 (.clk(clk_out), .D(d_ff_1_q), .Q(d_ff_2_q));  // open: Qn, preset, en, reset
  D_Flip_Flop d_ff_3 (.clk(clk_out), .D(d_ff_2_q), .Q(d_ff_3_q));  // open: Qn, preset, en, reset
  D_Flip_Flop d_ff_4 (.clk(clk_out), .D(d_ff_3_q), .Q(d_ff_4_q), .Qn(d_ff_4_qn));  // open: preset, en, reset
  or or_1 (or_1_out, d_ff_4_q, d_ff_4_qn);
  and and_1 (S, or_1_out, d_ff_3_q, d_ff_2_q, d_ff_1_q);

  // Notes on the sheet:
  //   João Henrique - 392734
endmodule

module Exemplo0056 (
  input  I,
  output S
);

  wire and_1_out, clk_out, d_ff_1_q, d_ff_2_q, d_ff_3_q, d_ff_4_q, nor_1_out;

  Clock clk (.out(clk_out));
  D_Flip_Flop d_ff_1 (.clk(clk_out), .D(I), .Q(d_ff_1_q));  // open: Qn, preset, en, reset
  D_Flip_Flop d_ff_2 (.clk(clk_out), .D(d_ff_1_q), .Q(d_ff_2_q));  // open: Qn, preset, en, reset
  D_Flip_Flop d_ff_3 (.clk(clk_out), .D(d_ff_2_q), .Q(d_ff_3_q));  // open: Qn, preset, en, reset
  D_Flip_Flop d_ff_4 (.clk(clk_out), .D(d_ff_3_q), .Q(d_ff_4_q));  // open: Qn, preset, en, reset
  and and_1 (and_1_out, d_ff_4_q, d_ff_3_q, d_ff_2_q, d_ff_1_q);
  nor nor_1 (nor_1_out, d_ff_4_q, d_ff_3_q, d_ff_2_q, d_ff_1_q);
  or or_1 (S, and_1_out, nor_1_out);

  // Notes on the sheet:
  //   João Henrique - 392734
endmodule
