// Logisim project Exemplo0054.circ as structural Verilog: 1 circuit, main circuit main
module main (
  input  \input ,
  input  clear,
  output \output 
);

  wire and_1_out, clk_out, d_ff_1_q, d_ff_1_qn, d_ff_2_q, d_ff_3_q, d_ff_4_q, not_1_out;

  Clock clk (.out(clk_out));
  and and_1 (and_1_out, not_1_out, clk_out);
  D_Flip_Flop d_ff_1 (
    .clk(and_1_out), .D(\input ), .Q(d_ff_1_q), .Qn(d_ff_1_qn), .en(not_1_out), .reset(clear));  // open: preset
  not not_1 (not_1_out, \output );
  D_Flip_Flop d_ff_2 (.clk(and_1_out), .D(d_ff_1_q), .Q(d_ff_2_q), .reset(clear));  // open: Qn, preset, en
  D_Flip_Flop d_ff_3 (.clk(and_1_out), .D(d_ff_2_q), .Q(d_ff_3_q), .en(not_1_out), .reset(clear));  // open: Qn, preset
  and and_2 (\output , d_ff_4_q, d_ff_3_q, d_ff_2_q, d_ff_1_qn);
  D_Flip_Flop d_ff_4 (.clk(and_1_out), .D(d_ff_3_q), .Q(d_ff_4_q), .en(not_1_out), .reset(clear));  // open: Qn, preset
endmodule
