// Logisim project Exemplo0052.circ as structural Verilog: 1 circuit, main circuit main
module main (
  input  D,
  input  Clear,
  output out_3
);

  wire Clock_out, d_ff_1_q, d_ff_2_q, d_ff_2_qn, d_ff_3_q, d_ff_3_qn, d_ff_4_q;

  Clock Clock (.out(Clock_out));
  D_Flip_Flop d_ff_1 (.clk(Clock_out), .D(D), .Q(d_ff_1_q), .reset(Clear));  // open: Qn, preset, en
  D_Flip_Flop d_ff_2 (.clk(Clock_out), .D(d_ff_1_q), .Q(d_ff_2_q), .Qn(d_ff_2_qn), .reset(Clear));  // open: preset, en
  and and_1 (out_3, d_ff_1_q, d_ff_2_qn, d_ff_3_qn, d_ff_4_q);
  D_Flip_Flop d_ff_3 (.clk(Clock_out), .D(d_ff_2_q), .Q(d_ff_3_q), .Qn(d_ff_3_qn), .reset(Clear));  // open: preset, en
  D_Flip_Flop d_ff_4 (.clk(Clock_out), .D(d_ff_3_q), .Q(d_ff_4_q), .reset(Clear));  // open: Qn, preset, en
endmodule
