// Logisim project Exemplo0054_logisim.circ as structural Verilog: 1 circuit, main circuit main
module main (
  input  clock,
  input  data,
  output reconheceu
);

  wire and_1_out, d_ff_1_q, d_ff_2_q, d_ff_3_q, d_ff_4_q, d_ff_5_q, not_1_out;

  D_Flip_Flop d_ff_1 (.clk(clock), .D(data), .Q(d_ff_1_q));  // open: Qn, preset, en, reset
  D_Flip_Flop d_ff_2 (.clk(clock), .D(d_ff_1_q), .Q(d_ff_2_q));  // open: Qn, preset, en, reset
  not not_1 (not_1_out, d_ff_1_q);
  and and_1 (and_1_out, not_1_out, d_ff_2_q, d_ff_3_q, d_ff_4_q);
  D_Flip_Flop d_ff_3 (.clk(clock), .D(d_ff_2_q), .Q(d_ff_3_q));  // open: Qn, preset, en, reset
  D_Flip_Flop d_ff_4 (.clk(clock), .D(d_ff_3_q), .Q(d_ff_4_q));  // open: Qn, preset, en, reset
  D_Flip_Flop d_ff_5 (.clk(clock), .D(and_1_out), .Q(d_ff_5_q));  // open: Qn, preset, en, reset
  or or_1 (reconheceu, d_ff_5_q, reconheceu);
endmodule
