// Logisim project FlipFlopD.circ as structural Verilog: 1 circuit, main circuit FlipFlopD
module FlipFlopD (
  input  enable,
  input  D,
  output Q,
  output QNot
);

  wire nand_1_out, nand_2_out, not_1_out;

  nand nand_1 (nand_1_out, D, enable);
  not not_1 (not_1_out, D);
  nand nand_2 (nand_2_out, not_1_out, enable);
  nor nor_1 (Q, nand_1_out, QNot);
  nor nor_2 (QNot, nand_2_out, Q);
endmodule
