// Logisim project Exemplo0054.circ as structural Verilog: 1 circuit, main circuit Rec1110
module Rec1110 (
  input  x,
  input  Reset,
  input  x_2,
  input  Reset_2,
  output Saida,
  output Saida_2
);

  wire and_2_out, Clk_2_out, Clk_out, d_ff_1_q, d_ff_2_q, d_ff_3_q, d_ff_4_q, d_ff_5_q, d_ff_6_q, d_ff_7_q,
       d_ff_8_q, not_1_out, not_2_out;

  Clock Clk (.out(Clk_out));
  Clock Clk_2 (.out(Clk_2_out));
  D_Flip_Flop d_ff_1 (.clk(Clk_out), .D(x), .Q(d_ff_1_q), .reset(Reset));  // open: Qn, preset, en
  D_Flip_Flop d_ff_2 (.clk(Clk_out), .D(d_ff_1_q), .Q(d_ff_2_q), .reset(Reset));  // open: Qn, preset, en
  D_Flip_Flop d_ff_3 (.clk(Clk_2_out), .D(x_2), .Q(d_ff_3_q), .reset(Reset_2));  // open: Qn, preset, en
  D_Flip_Flop d_ff_4 (.clk(Clk_out), .D(d_ff_2_q), .Q(d_ff_4_q), .reset(Reset));  // open: Qn, preset, en
  not not_1 (not_1_out, d_ff_1_q);
  and and_1 (Saida, not_1_out, d_ff_2_q, d_ff_4_q, d_ff_6_q);
  D_Flip_Flop d_ff_5 (.clk(Clk_2_out), .D(d_ff_3_q), .Q(d_ff_5_q), .reset(Reset_2));  // open: Qn, preset, en
  not not_2 (not_2_out, d_ff_3_q);
  and and_2 (and_2_out, not_2_out, d_ff_5_q, d_ff_7_q, d_ff_8_q);
  D_Flip_Flop d_ff_6 (.clk(Clk_out), .D(d_ff_4_q), .Q(d_ff_6_q), .reset(Reset));  // open: Qn, preset, en
  D_Flip_Flop d_ff_7 (.clk(Clk_2_out), .D(d_ff_5_q), .Q(d_ff_7_q), .reset(Reset_2));  // open: Qn, preset, en
  D_Flip_Flop d_ff_8 (.clk(Clk_2_out), .D(d_ff_7_q), .Q(d_ff_8_q), .reset(Reset_2));  // open: Qn, preset, en
  D_Flip_Flop d_ff_9 (.clk(Clk_2_out), .D(and_2_out), .Q(Saida_2), .reset(Reset_2));  // open: Qn, preset, en
endmodule
