// Logisim project Exemplo0052.circ as structural Verilog: 1 circuit, main circuit main
module main (
  input  CLK,
  input  X,
  input  RESET,
  input  CLK_2,
  input  X_2,
  input  RESET_2,
  output Y,
  output Y_2
);

  wire d_ff_1_q, d_ff_2_q, d_ff_3_q, d_ff_4_q, d_ff_4_qn, d_ff_5_q, d_ff_6_q, d_ff_6_qn, d_ff_7_q, d_ff_8_q,
       not_1_out, not_2_out;

  D_Flip_Flop d_ff_1 (.clk(CLK), .D(X), .Q(d_ff_1_q), .reset(RESET));  // open: Qn, preset, en
  D_Flip_Flop d_ff_2 (.clk(CLK_2), .D(X_2), .Q(d_ff_2_q), .reset(RESET_2));  // open: Qn, preset, en
  D_Flip_Flop d_ff_3 (.clk(CLK), .D(d_ff_1_q), .Q(d_ff_3_q), .reset(RESET));  // open: Qn, preset, en
  D_Flip_Flop d_ff_4 (.clk(CLK_2), .D(d_ff_2_q), .Q(d_ff_4_q), .Qn(d_ff_4_qn), .reset(RESET_2));  // open: preset, en
  D_Flip_Flop d_ff_5 (.clk(CLK), .D(d_ff_3_q), .Q(d_ff_5_q), .reset(RESET));  // open: Qn, preset, en
  not not_1 (not_1_out, d_ff_5_q);
  not not_2 (not_2_out, d_ff_3_q);
  and and_1 (Y, d_ff_1_q, not_2_out, not_1_out, d_ff_7_q);
  D_Flip_Flop d_ff_6 (.clk(CLK_2), .D(d_ff_4_q), .Q(d_ff_6_q), .Qn(d_ff_6_qn), .reset(RESET_2));  // open: preset, en
  and and_2 (Y_2, d_ff_2_q, d_ff_4_qn, d_ff_6_qn, d_ff_8_q);
  D_Flip_Flop d_ff_7 (.clk(CLK), .D(d_ff_5_q), .Q(d_ff_7_q), .reset(RESET));  // open: Qn, preset, en
  D_Flip_Flop d_ff_8 (.clk(CLK_2), .D(d_ff_6_q), .Q(d_ff_8_q), .reset(RESET_2));  // open: Qn, preset, en

  // Notes on the sheet:
  //   OU
  //   1-reconhece-1001   e
  //    1001001
  //   1-reconhece-1001   e
  //    1001001
endmodule
