// Logisim project Exemplo0053.circ as structural Verilog: 1 circuit, main circuit main
module main (
  input  CLK,
  input  X,
  input  RESET,
  output Y
);

  wire and_1_out, d_ff_1_q, d_ff_2_q, d_ff_2_qn, d_ff_3_q, d_ff_3_qn, d_ff_4_q, not_1_out;

  D_Flip_Flop d_ff_1 (.clk(CLK), .D(X), .Q(d_ff_1_q), .en(not_1_out), .reset(RESET));  // open: Qn, preset
  D_Flip_Flop d_ff_2 (.clk(CLK), .D(d_ff_1_q), .Q(d_ff_2_q), .Qn(d_ff_2_qn), .reset(RESET));  // open: preset, en
  D_Flip_Flop d_ff_3 (.clk(CLK), .D(d_ff_2_q), .Q(d_ff_3_q), .Qn(d_ff_3_qn), .reset(RESET));  // open: preset, en
  and and_1 (and_1_out, d_ff_4_q, d_ff_3_qn, d_ff_2_qn, d_ff_1_q);
  D_Flip_Flop d_ff_4 (.clk(CLK), .D(d_ff_3_q), .Q(d_ff_4_q), .reset(RESET));  // open: Qn, preset, en
  D_Flip_Flop d_ff_5 (.clk(CLK), .D(and_1_out), .Q(Y), .reset(RESET));  // open: Qn, preset, en
  not not_1 (not_1_out, Y);
endmodule
