// Logisim project Circuitos.circ as structural Verilog
module Mealy1101 (
  input  x,
  input  clear,
  output out_3
);

  wire clock_out, d_ff_1_q, d_ff_2_q, d_ff_2_qn, d_ff_3_q, d_ff_4_q;

  Clock clock (.out(clock_out));
  D_Flip_Flop d_ff_1 (.clk(clock_out), .D(x), .Q(d_ff_1_q), .reset(clear));  // open: Qn, preset, en
  D_Flip_Flop d_ff_2 (.clk(clock_out), .D(d_ff_1_q), .Q(d_ff_2_q), .Qn(d_ff_2_qn), .reset(clear));  // open: preset, en
  and and_1 (out_3, d_ff_1_q, d_ff_2_qn, d_ff_3_q, d_ff_4_q);
  D_Flip_Flop d_ff_3 (.clk(clock_out), .D(d_ff_2_q), .Q(d_ff_3_q), .reset(clear));  // open: Qn, preset, en
  D_Flip_Flop d_ff_4 (.clk(clock_out), .D(d_ff_3_q), .Q(d_ff_4_q), .reset(clear));  // open: Qn, preset, en
endmodule

module Moore1101 (
  input  x,
  input  clear,
  output out_3
);

  wire and_1_out, clock_out, d_ff_1_q, d_ff_2_q, d_ff_2_qn, d_ff_3_q, d_ff_4_q;

  Clock clock (.out(clock_out));
  D_Flip_Flop d_ff_1 (.clk(clock_out), .D(x), .Q(d_ff_1_q), .reset(clear));  // open: Qn, preset, en
  D_Flip_Flop d_ff_2 (.clk(clock_out), .D(d_ff_1_q), .Q(d_ff_2_q), .Qn(d_ff_2_qn), .reset(clear));  // open: preset, en
  and and_1 (and_1_out, d_ff_1_q, d_ff_2_qn, d_ff_3_q, d_ff_4_q);
  D_Flip_Flop d_ff_3 (.clk(clock_out), .D(d_ff_2_q), .Q(d_ff_3_q), .reset(clear));  // open: Qn, preset, en
  D_Flip_Flop d_ff_4 (.clk(clock_out), .D(d_ff_3_q), .Q(d_ff_4_q), .reset(clear));  // open: Qn, preset, en
  D_Flip_Flop d_ff_5 (.clk(clock_out), .D(and_1_out), .Q(out_3), .reset(clear));  // open: Qn, preset, en
endmodule

module Exemplo0052 (
  input  x,
  input  clear,
  output out_3
);

  wire clock_out, d_ff_1_q, d_ff_2_q, d_ff_2_qn, d_ff_3_q, d_ff_3_qn, d_ff_4_q;

  Clock clock (.out(clock_out));
  D_Flip_Flop d_ff_1 (.clk(clock_out), .D(x), .Q(d_ff_1_q), .reset(clear));  // open: Qn, preset, en
  D_Flip_Flop d_ff_2 (.clk(clock_out), .D(d_ff_1_q), .Q(d_ff_2_q), .Qn(d_ff_2_qn), .reset(clear));  // open: preset, en
  and and_1 (out_3, d_ff_1_q, d_ff_2_qn, d_ff_3_qn, d_ff_4_q);
  D_Flip_Flop d_ff_3 (.clk(clock_out), .D(d_ff_2_q), .Q(d_ff_3_q), .Qn(d_ff_3_qn), .reset(clear));  // open: preset, en
  D_Flip_Flop d_ff_4 (.clk(clock_out), .D(d_ff_3_q), .Q(d_ff_4_q), .reset(clear));  // open: Qn, preset, en
endmodule

module Exemplo0053 (
  input  x,
  input  clear,
  output s
);

  wire and_1_out, and_2_out, clock_out, d_ff_1_q, d_ff_2_q, d_ff_3_q, d_ff_4_qn, or_1_out;

  Clock clock (.out(clock_out));
  or or_1 (or_1_out, clear, s);
  D_Flip_Flop d_ff_1 (.clk(clock_out), .D(x), .Q(d_ff_1_q), .reset(and_1_out));  // open: Qn, preset, en
  and and_1 (and_1_out, clock_out, or_1_out);
  D_Flip_Flop d_ff_2 (.clk(clock_out), .D(d_ff_1_q), .Q(d_ff_2_q), .reset(and_1_out));  // open: Qn, preset, en
  and and_2 (and_2_out, d_ff_1_q, d_ff_2_q, d_ff_3_q, d_ff_4_qn);
  D_Flip_Flop d_ff_3 (.clk(clock_out), .D(d_ff_2_q), .Q(d_ff_3_q), .reset(and_1_out));  // open: Qn, preset, en
  D_Flip_Flop d_ff_4 (.clk(clock_out), .D(d_ff_3_q), .Qn(d_ff_4_qn), .reset(and_1_out));  // open: Q, preset, en
  D_Flip_Flop d_ff_5 (.clk(clock_out), .D(and_2_out), .Q(s), .reset(clear));  // open: Qn, preset, en
endmodule

module Exemplo0054 (
  input  x,
  input  clear,
  output s
);

  wire and_1_out, and_2_out, clock_out, d_ff_1_q, d_ff_2_q, d_ff_3_q, d_ff_4_qn, or_1_out;

  Clock clock (.out(clock_out));
  or or_1 (or_1_out, clear, s);
  D_Flip_Flop d_ff_1 (.clk(clock_out), .D(x), .Q(d_ff_1_q), .reset(and_1_out));  // open: Qn, preset, en
  and and_1 (and_1_out, clock_out, or_1_out);
  D_Flip_Flop d_ff_2 (.clk(clock_out), .D(d_ff_1_q), .Q(d_ff_2_q), .reset(and_1_out));  // open: Qn, preset, en
  and and_2 (and_2_out, d_ff_1_q, d_ff_2_q, d_ff_3_q, d_ff_4_qn);
  D_Flip_Flop d_ff_3 (.clk(clock_out), .D(d_ff_2_q), .Q(d_ff_3_q), .reset(and_1_out));  // open: Qn, preset, en
  D_Flip_Flop d_ff_4 (.clk(clock_out), .D(d_ff_3_q), .Qn(d_ff_4_qn), .reset(and_1_out));  // open: Q, preset, en
  D_Flip_Flop d_ff_5 (.clk(clock_out), .D(and_2_out), .Q(s), .reset(clear));  // open: Qn, preset, en
endmodule

module Exemplo0055 (
  input  x,
  input  clear,
  output out_3
);

  wire clock_out, d_ff_1_q, d_ff_1_qn, d_ff_2_q, d_ff_2_qn, d_ff_3_q, d_ff_3_qn;

  Clock clock (.out(clock_out));
  D_Flip_Flop d_ff_1 (.clk(clock_out), .D(x), .Q(d_ff_1_q), .Qn(d_ff_1_qn), .reset(clear));  // open: preset, en
  D_Flip_Flop d_ff_2 (.clk(clock_out), .D(d_ff_1_q), .Q(d_ff_2_q), .Qn(d_ff_2_qn), .reset(clear));  // open: preset, en
  and and_1 (out_3, d_ff_1_qn, d_ff_2_qn, d_ff_3_qn);
  D_Flip_Flop d_ff_3 (.clk(clock_out), .D(d_ff_2_q), .Q(d_ff_3_q), .Qn(d_ff_3_qn), .reset(clear));  // open: preset, en
  D_Flip_Flop d_ff_4 (.clk(clock_out), .D(d_ff_3_q), .reset(clear));  // open: Q, Qn, preset, en
endmodule

module Exemplo0056 (
  input  x,
  input  clear,
  output out_3
);

  wire and_1_out, and_2_out, clock_out, d_ff_1_q, d_ff_1_qn, d_ff_2_q, d_ff_2_qn, d_ff_3_q, d_ff_3_qn;

  Clock clock (.out(clock_out));
  D_Flip_Flop d_ff_1 (.clk(clock_out), .D(x), .Q(d_ff_1_q), .Qn(d_ff_1_qn), .reset(clear));  // open: preset, en
  D_Flip_Flop d_ff_2 (.clk(clock_out), .D(d_ff_1_q), .Q(d_ff_2_q), .Qn(d_ff_2_qn), .reset(clear));  // open: preset, en
  and and_1 (and_1_out, d_ff_1_qn, d_ff_2_qn, d_ff_3_qn);
  D_Flip_Flop d_ff_3 (.clk(clock_out), .D(d_ff_2_q), .Q(d_ff_3_q), .Qn(d_ff_3_qn), .reset(clear));  // open: preset, en
  and and_2 (and_2_out, d_ff_1_q, d_ff_2_q, d_ff_3_q);
  or or_1 (out_3, and_1_out, and_2_out);
endmodule
