// Logisim project Exemplo0053.circ as structural Verilog: 1 circuit, main circuit Exemplo0053
module Exemplo0053 (
  input  entrada,
  input  clear,
  output saida
);

  wire and_1_out, clock_out, d_ff_1_q, d_ff_2_q, d_ff_2_qn, d_ff_3_q, d_ff_3_qn, d_ff_4_q, or_1_out;

  Clock clock (.out(clock_out));
  or or_1 (or_1_out, clear, saida);
  D_Flip_Flop d_ff_1 (.clk(clock_out), .D(entrada), .Q(d_ff_1_q), .reset(or_1_out));  // open: Qn, preset, en
  D_Flip_Flop d_ff_2 (
    .clk(clock_out), .D(d_ff_1_q), .Q(d_ff_2_q), .Qn(d_ff_2_qn), .reset(or_1_out));  // open: preset, en
  D_Flip_Flop d_ff_3 (
    .clk(clock_out), .D(d_ff_2_q), .Q(d_ff_3_q), .Qn(d_ff_3_qn), .reset(or_1_out));  // open: preset, en
  and and_1 (and_1_out, d_ff_1_q, d_ff_2_qn, d_ff_3_qn, d_ff_4_q);
  D_Flip_Flop d_ff_4 (.clk(clock_out), .D(d_ff_3_q), .Q(d_ff_4_q), .reset(or_1_out));  // open: Qn, preset, en
  D_Flip_Flop d_ff_5 (.clk(clock_out), .D(and_1_out), .Q(saida));  // open: Qn, preset, en, reset

  // Notes on the sheet:
  //   Exemplo0053
  //   Ana Cristina - 427385
endmodule
