// Logisim project Exemplo0054.circ as structural Verilog: 1 circuit, main circuit Exemplo0054
module Exemplo0054 (
  input  entrada,
  input  clear,
  output saida
);

  wire clock_out, d_ff_1_q, d_ff_1_qn, d_ff_2_q, d_ff_3_q, d_ff_4_q;

  Clock clock (.out(clock_out));
  D_Flip_Flop d_ff_1 (.clk(clock_out), .D(entrada), .Q(d_ff_1_q), .Qn(d_ff_1_qn), .reset(clear));  // open: preset, en
  D_Flip_Flop d_ff_2 (.clk(clock_out), .D(d_ff_1_q), .Q(d_ff_2_q), .reset(clear));  // open: Qn, preset, en
  D_Flip_Flop d_ff_3 (.clk(clock_out), .D(d_ff_2_q), .Q(d_ff_3_q), .reset(clear));  // open: Qn, preset, en
  D_Flip_Flop d_ff_4 (.clk(clock_out), .D(d_ff_3_q), .Q(d_ff_4_q), .reset(clear));  // open: Qn, preset, en
  and and_1 (saida, d_ff_4_q, d_ff_3_q, d_ff_2_q, d_ff_1_qn);

  // Notes on the sheet:
  //   Exemplo0054
  //   Ana Cristina - 427385
endmodule
