// Logisim project Exemplo0055.circ as structural Verilog: 1 circuit, main circuit Exemplo0055
module Exemplo0055 (
  input  entrada,
  input  clear,
  output saida
);

  wire and_1_out, clock_out, d_ff_1_q, d_ff_1_qn, d_ff_2_q, d_ff_2_qn, d_ff_3_q, d_ff_3_qn, d_ff_4_q,
       d_ff_4_qn, or_1_out;

  Clock clock (.out(clock_out));
  D_Flip_Flop d_ff_1 (.clk(clock_out), .D(entrada), .Q(d_ff_1_q), .Qn(d_ff_1_qn), .reset(clear));  // open: preset, en
  D_Flip_Flop d_ff_2 (.clk(clock_out), .D(d_ff_1_q), .Q(d_ff_2_q), .Qn(d_ff_2_qn), .reset(clear));  // open: preset, en
  and and_1 (and_1_out, d_ff_1_qn, d_ff_2_qn, d_ff_3_qn);
  D_Flip_Flop d_ff_3 (.clk(clock_out), .D(d_ff_2_q), .Q(d_ff_3_q), .Qn(d_ff_3_qn), .reset(clear));  // open: preset, en
  D_Flip_Flop d_ff_4 (.clk(clock_out), .D(d_ff_3_q), .Q(d_ff_4_q), .Qn(d_ff_4_qn), .reset(clear));  // open: preset, en
  or or_1 (or_1_out, d_ff_4_q, d_ff_4_qn);
  and and_2 (saida, or_1_out, and_1_out);

  // Notes on the sheet:
  //   Exemplo0055
  //   Ana Cristina - 427385
endmodule
