// Logisim project Exemplo0052.circ as structural Verilog: 1 circuit, main circuit main
module main (
  input  in_1,
  input  in_2,
  output [7:0] out_3
);

  wire and_1_out, clock_1_out, not_1_out, not_2_out;

  Clock clock_1 (.out(clock_1_out));
  LED led_1 (.in(and_1_out));
  D_Flip_Flop d_ff_1 (.clk(clock_1_out), .D(in_1), .Q(out_3[0]), .reset(in_2));  // open: Qn, preset, en
  D_Flip_Flop d_ff_2 (.clk(clock_1_out), .D(out_3[0]), .Q(out_3[1]), .reset(in_2));  // open: Qn, preset, en
  D_Flip_Flop d_ff_3 (.clk(clock_1_out), .D(out_3[1]), .Q(out_3[2]), .reset(in_2));  // open: Qn, preset, en
  D_Flip_Flop d_ff_4 (.clk(clock_1_out), .D(out_3[3]), .Q(out_3[4]), .reset(in_2));  // open: Qn, preset, en
  D_Flip_Flop d_ff_5 (.clk(clock_1_out), .D(out_3[2]), .Q(out_3[3]), .reset(in_2));  // open: Qn, preset, en
  D_Flip_Flop d_ff_6 (.clk(clock_1_out), .D(out_3[4]), .Q(out_3[5]), .reset(in_2));  // open: Qn, preset, en
  D_Flip_Flop d_ff_7 (.clk(clock_1_out), .D(out_3[5]), .Q(out_3[6]), .reset(in_2));  // open: Qn, preset, en
  D_Flip_Flop d_ff_8 (.clk(clock_1_out), .D(out_3[6]), .Q(out_3[7]), .reset(in_2));  // open: Qn, preset, en
  not not_1 (not_1_out, out_3[1]);
  not not_2 (not_2_out, out_3[2]);
  and and_1 (and_1_out, out_3[0], not_1_out, not_2_out, out_3[3]);
endmodule
