// Logisim project Exemplo0052comContador.circ as structural Verilog: 7 circuits, main circuit main
module main (
  input  in_1,
  input  in_2,
  output [7:0] out_3
);

  wire and_1_out, clock_1_out, not_1_out, not_2_out;

  Clock clock_1 (.out(clock_1_out));
  LED led_1 (.in(and_1_out));
  D_Flip_Flop d_ff_1 (.clk(clock_1_out), .D(in_1), .Q(out_3[0]), .reset(in_2));  // open: Qn, preset, en
  D_Flip_Flop d_ff_2 (.clk(clock_1_out), .D(out_3[0]), .Q(out_3[1]), .reset(in_2));  // open: Qn, preset, en
  D_Flip_Flop d_ff_3 (.clk(clock_1_out), .D(out_3[1]), .Q(out_3[2]), .reset(in_2));  // open: Qn, preset, en
  D_Flip_Flop d_ff_4 (.clk(clock_1_out), .D(out_3[2]), .Q(out_3[3]), .reset(in_2));  // open: Qn, preset, en
  D_Flip_Flop d_ff_5 (.clk(clock_1_out), .D(out_3[4]), .Q(out_3[5]), .reset(in_2));  // open: Qn, preset, en
  D_Flip_Flop d_ff_6 (.clk(clock_1_out), .D(out_3[3]), .Q(out_3[4]), .reset(in_2));  // open: Qn, preset, en
  D_Flip_Flop d_ff_7 (.clk(clock_1_out), .D(out_3[5]), .Q(out_3[6]), .reset(in_2));  // open: Qn, preset, en
  D_Flip_Flop d_ff_8 (.clk(clock_1_out), .D(out_3[6]), .Q(out_3[7]), .reset(in_2));  // open: Qn, preset, en
  not not_1 (not_1_out, out_3[1]);
  not not_2 (not_2_out, out_3[2]);
  and and_1 (and_1_out, out_3[0], not_1_out, not_2_out, out_3[3]);
endmodule

module halfAdder (
  input  Carry_In,
  input  a,
  output s,
  output Carry_Out
);

  xor xor_1 (Carry_Out, Carry_In, a);
  and and_1 (s, Carry_In, a);
endmodule

module fullAdder (
  input  Carry_In,
  input  a,
  input  b,
  output Saida,
  output Carry_Out
);

  wire halfadder_1_carry_out, halfadder_1_s, halfadder_2_s;

  halfAdder halfadder_1 (.a(a), .Carry_In(Carry_In), .Carry_Out(halfadder_1_carry_out), .s(halfadder_1_s));
  halfAdder halfadder_2 (.a(b), .Carry_In(halfadder_1_carry_out), .Carry_Out(Saida), .s(halfadder_2_s));
  or or_1 (Carry_Out, halfadder_1_s, halfadder_2_s);
endmodule

module fullAdder4Bits (
  input  [3:0] a,
  input  [3:0] b,
  input  C_In,
  output [3:0] Saida,
  output Carry_Out
);

  wire fulladder_1_carry_out, fulladder_2_carry_out, fulladder_3_carry_out;

  fullAdder fulladder_1 (.a(b[0]), .b(a[0]), .Carry_In(C_In), .Carry_Out(fulladder_1_carry_out), .Saida(Saida[0]));
  fullAdder fulladder_2 (
    .a(b[1]), .b(a[1]), .Carry_In(fulladder_1_carry_out), .Carry_Out(fulladder_2_carry_out), .Saida(Saida[1]));
  fullAdder fulladder_3 (
    .a(b[2]), .b(a[2]), .Carry_In(fulladder_2_carry_out), .Carry_Out(fulladder_3_carry_out), .Saida(Saida[2]));
  fullAdder fulladder_4 (.a(b[3]), .b(a[3]), .Carry_In(fulladder_3_carry_out), .Carry_Out(Carry_Out), .Saida(Saida[3]));
endmodule

module fullAdder8Bits (
  input  [7:0] a,
  input  [7:0] b,
  input  carry_in,
  output [7:0] Saida,
  output Carry_Out
);

  wire fulladder4bits_1_carry_out;

  fullAdder4Bits fulladder4bits_1 (
    .a(a[3:0]), .b(b[3:0]), .C_In(carry_in), .Carry_Out(fulladder4bits_1_carry_out), .Saida(Saida[3:0]));
  fullAdder4Bits fulladder4bits_2 (
    .a(b[7:4]), .b(a[7:4]), .C_In(fulladder4bits_1_carry_out), .Carry_Out(Carry_Out), .Saida(Saida[7:4]));
endmodule

module auxiliar (
  input  [7:0] a,
  input  [7:0] b,
  input  C_In,
  output [7:0] saida,
  output Carry_Out
);

  wire fulladder_1_carry_out, fulladder_2_carry_out, fulladder_3_carry_out, fulladder_4_carry_out,
       fulladder_5_carry_out, fulladder_6_carry_out, fulladder_7_carry_out;

  fullAdder fulladder_1 (.a(a[0]), .b(b[0]), .Carry_In(C_In), .Carry_Out(fulladder_1_carry_out), .Saida(saida[0]));
  fullAdder fulladder_2 (
    .a(a[1]), .b(b[1]), .Carry_In(fulladder_1_carry_out), .Carry_Out(fulladder_2_carry_out), .Saida(saida[1]));
  fullAdder fulladder_3 (
    .a(a[2]), .b(b[2]), .Carry_In(fulladder_2_carry_out), .Carry_Out(fulladder_3_carry_out), .Saida(saida[2]));
  fullAdder fulladder_4 (
    .a(a[3]), .b(b[3]), .Carry_In(fulladder_3_carry_out), .Carry_Out(fulladder_4_carry_out), .Saida(saida[3]));
  fullAdder fulladder_5 (
    .a(a[4]), .b(b[4]), .Carry_In(fulladder_4_carry_out), .Carry_Out(fulladder_5_carry_out), .Saida(saida[4]));
  fullAdder fulladder_6 (
    .a(a[5]), .b(b[5]), .Carry_In(fulladder_5_carry_out), .Carry_Out(fulladder_6_carry_out), .Saida(saida[5]));
  fullAdder fulladder_7 (
    .a(a[6]), .b(b[6]), .Carry_In(fulladder_6_carry_out), .Carry_Out(fulladder_7_carry_out), .Saida(saida[6]));
  fullAdder fulladder_8 (.a(a[7]), .b(b[7]), .Carry_In(fulladder_7_carry_out), .Carry_Out(Carry_Out), .Saida(saida[7]));
endmodule

module questao_da_Prova (
  input  in_1,
  input  in_2,
  input  in_3,
  input  in_4,
  output out_5
);

  wire and_1_out, and_2_out, and_3_out, and_4_out, clock_1_out, j_k_ff_1_q, j_k_ff_1_qn, j_k_ff_2_q,
       j_k_ff_2_qn, j_k_ff_3_q, not_1_out, not_2_out, not_3_out, not_4_out;

  Clock clock_1 (.out(clock_1_out));
  J_K_Flip_Flop j_k_ff_1 (
    .J(in_1), .clk(clock_1_out), .K(in_2), .Q(j_k_ff_1_q), .Qn(j_k_ff_1_qn), .reset(in_4));  // open: preset, en
  J_K_Flip_Flop j_k_ff_2 (
    .J(j_k_ff_1_q), .clk(clock_1_out), .K(j_k_ff_1_qn), .Q(j_k_ff_2_q), .Qn(j_k_ff_2_qn), .reset(in_4));  // open: preset, en
  J_K_Flip_Flop j_k_ff_3 (
    .J(j_k_ff_2_q), .clk(clock_1_out), .K(j_k_ff_2_qn), .Q(j_k_ff_3_q), .reset(in_4));  // open: Qn, preset, en
  not not_1 (not_1_out, j_k_ff_2_q);
  and and_1 (and_1_out, j_k_ff_1_q, not_1_out, j_k_ff_3_q);
  not not_2 (not_2_out, j_k_ff_1_q);
  not not_3 (not_3_out, j_k_ff_2_q);
  not not_4 (not_4_out, in_3);
  and and_2 (and_2_out, not_2_out, not_3_out, j_k_ff_3_q);
  and and_3 (and_3_out, in_3, and_1_out);
  and and_4 (and_4_out, not_4_out, and_2_out);
  or or_1 (out_5, and_3_out, and_4_out);
endmodule
