// Logisim project Questao2Prova1.circ as structural Verilog: 1 circuit, main circuit main
module main (
  input  [1:0] in_1,
  input  in_2,
  input  in_3
);

  wire and_1_out, and_2_out, and_3_out, and_4_out, clock_1_out, j_k_ff_1_q, j_k_ff_1_qn, j_k_ff_2_q,
       j_k_ff_2_qn, j_k_ff_3_q, not_1_out, not_2_out, not_3_out, not_4_out, or_1_out;

  Clock clock_1 (.out(clock_1_out));
  J_K_Flip_Flop j_k_ff_1 (
    .J(in_1[0]), .clk(clock_1_out), .K(in_1[1]), .Q(j_k_ff_1_q), .Qn(j_k_ff_1_qn), .reset(in_2));  // open: preset, en
  J_K_Flip_Flop j_k_ff_2 (
    .J(j_k_ff_1_q), .clk(clock_1_out), .K(j_k_ff_1_qn), .Q(j_k_ff_2_q), .Qn(j_k_ff_2_qn), .reset(in_2));  // open: preset, en
  J_K_Flip_Flop j_k_ff_3 (
    .J(j_k_ff_2_q), .clk(clock_1_out), .K(j_k_ff_2_qn), .Q(j_k_ff_3_q), .reset(in_2));  // open: Qn, preset, en
  not not_1 (not_1_out, j_k_ff_2_q);
  and and_1 (and_1_out, j_k_ff_1_q, not_1_out, j_k_ff_3_q);
  not not_2 (not_2_out, j_k_ff_1_q);
  not not_3 (not_3_out, j_k_ff_2_q);
  and and_2 (and_2_out, not_2_out, not_3_out, j_k_ff_3_q);
  and and_3 (and_3_out, in_3, and_1_out);
  not not_4 (not_4_out, in_3);
  and and_4 (and_4_out, not_4_out, and_2_out);
  LED led_1 (.in(or_1_out));
  or or_1 (or_1_out, and_3_out, and_4_out);
endmodule
