// Logisim project guia0803.circ as structural Verilog: 1 circuit, main circuit main
module main (
  input  clk,
  input  data,
  input  clr,
  output a,
  output b,
  output c,
  output d
);

  D_Flip_Flop d_ff_1 (.clk(clk), .D(data), .Q(a), .reset(clr));  // open: Qn, preset, en
  D_Flip_Flop d_ff_2 (.clk(clk), .D(a), .Q(b), .reset(clr));  // open: Qn, preset, en
  D_Flip_Flop d_ff_3 (.clk(clk), .D(b), .Q(c), .reset(clr));  // open: Qn, preset, en
  D_Flip_Flop d_ff_4 (.clk(clk), .D(c), .Q(d), .reset(clr));  // open: Qn, preset, en
endmodule
