// Logisim project guia0805.circ as structural Verilog: 1 circuit, main circuit main
module main (
  input  clk,
  input  in_2,
  input  clr,
  input  LD,
  input  d3,
  input  d2,
  input  d1,
  input  d0,
  output a,
  output b,
  output c,
  output d
);

  wire and_1_out, and_2_out, and_3_out, and_4_out;

  D_Flip_Flop d_ff_1 (.clk(clk), .D(in_2), .Q(a), .preset(and_1_out), .reset(clr));  // open: Qn, en
  and and_1 (and_1_out, LD, d3);
  and and_2 (and_2_out, LD, d2);
  D_Flip_Flop d_ff_2 (.clk(clk), .D(a), .Q(b), .preset(and_2_out), .reset(clr));  // open: Qn, en
  D_Flip_Flop d_ff_3 (.clk(clk), .D(b), .Q(c), .preset(and_3_out), .reset(clr));  // open: Qn, en
  and and_3 (and_3_out, LD, d1);
  D_Flip_Flop d_ff_4 (.clk(clk), .D(c), .Q(d), .preset(and_4_out), .reset(clr));  // open: Qn, en
  and and_4 (and_4_out, LD, d0);
endmodule
