// Logisim project Projetos.circ as structural Verilog
module Exercicio081 (
  input  D,
  input  RST,
  output S4,
  output S3,
  output S2,
  output S1,
  output S0
);

  wire CLK_out;

  Clock CLK (.out(CLK_out));
  D_Flip_Flop _4 (.clk(CLK_out), .D(S3), .Q(S4), .reset(RST));  // open: Qn, preset, en
  D_Flip_Flop _3 (.clk(CLK_out), .D(S2), .Q(S3), .reset(RST));  // open: Qn, preset, en
  D_Flip_Flop _2 (.clk(CLK_out), .D(S1), .Q(S2), .reset(RST));  // open: Qn, preset, en
  D_Flip_Flop _1 (.clk(CLK_out), .D(S0), .Q(S1), .reset(RST));  // open: Qn, preset, en
  D_Flip_Flop _0 (.clk(CLK_out), .D(D), .Q(S0), .reset(RST));  // open: Qn, preset, en
endmodule

module Exercicio082 (
  input  D,
  input  RST,
  output S4,
  output S3,
  output S2,
  output S1,
  output S0
);

  wire CLK_out, or_1_out, or_2_out, or_3_out, or_4_out;

  Clock CLK (.out(CLK_out));
  or or_1 (or_1_out, S3, D);
  D_Flip_Flop d_ff_1 (.clk(CLK_out), .D(or_1_out), .Q(S4), .reset(RST));  // open: Qn, preset, en
  D_Flip_Flop d_ff_2 (.clk(CLK_out), .D(or_2_out), .Q(S3), .reset(RST));  // open: Qn, preset, en
  or or_2 (or_2_out, S2, D);
  or or_3 (or_3_out, S1, D);
  D_Flip_Flop d_ff_3 (.clk(CLK_out), .D(or_3_out), .Q(S2), .reset(RST));  // open: Qn, preset, en
  D_Flip_Flop d_ff_4 (.clk(CLK_out), .D(or_4_out), .Q(S1), .reset(RST));  // open: Qn, preset, en
  or or_4 (or_4_out, S0, D);
  D_Flip_Flop d_ff_5 (.clk(CLK_out), .D(D), .Q(S0), .reset(RST));  // open: Qn, preset, en
endmodule

module Exercicio083 (
  input  D,
  input  RST,
  output S4,
  output S3,
  output S2,
  output S1,
  output S0
);

  wire CLK_out;

  Clock CLK (.out(CLK_out));
  D_Flip_Flop d_ff_1 (.clk(CLK_out), .D(D), .Q(S4), .reset(RST));  // open: Qn, preset, en
  D_Flip_Flop d_ff_2 (.clk(CLK_out), .D(S4), .Q(S3), .reset(RST));  // open: Qn, preset, en
  D_Flip_Flop d_ff_3 (.clk(CLK_out), .D(S3), .Q(S2), .reset(RST));  // open: Qn, preset, en
  D_Flip_Flop d_ff_4 (.clk(CLK_out), .D(S2), .Q(S1), .reset(RST));  // open: Qn, preset, en
  D_Flip_Flop d_ff_5 (.clk(CLK_out), .D(S1), .Q(S0), .reset(RST));  // open: Qn, preset, en
endmodule

module Exercicio084 (
  input  D,
  input  RST,
  output S4,
  output S3,
  output S2,
  output S1,
  output S0
);

  wire CLK_out, or_1_out;

  Clock CLK (.out(CLK_out));
  D_Flip_Flop d_ff_1 (.clk(CLK_out), .D(S3), .Q(S4), .reset(RST));  // open: Qn, preset, en
  or or_1 (or_1_out, S4, D);
  D_Flip_Flop d_ff_2 (.clk(CLK_out), .D(S2), .Q(S3), .reset(RST));  // open: Qn, preset, en
  D_Flip_Flop d_ff_3 (.clk(CLK_out), .D(S1), .Q(S2), .reset(RST));  // open: Qn, preset, en
  D_Flip_Flop d_ff_4 (.clk(CLK_out), .D(S0), .Q(S1), .reset(RST));  // open: Qn, preset, en
  D_Flip_Flop d_ff_5 (.clk(CLK_out), .D(or_1_out), .Q(S0), .reset(RST));  // open: Qn, preset, en
endmodule

module Exercicio085 (
  input  RST,
  input  LOAD,
  input  D4,
  input  D3,
  input  D2,
  input  D1,
  input  D0,
  output S4,
  output S3,
  output S2,
  output S1,
  output S0
);

  wire and_1_out, and_2_out, and_3_out, and_4_out, and_5_out, CLK_out;

  Clock CLK (.out(CLK_out));
  D_Flip_Flop d_ff_1 (.clk(CLK_out), .D(1'b0), .Q(S4), .preset(and_1_out), .reset(RST));  // open: Qn, en
  and and_1 (and_1_out, LOAD, D4);
  and and_2 (and_2_out, LOAD, D3);
  D_Flip_Flop d_ff_2 (.clk(CLK_out), .D(S4), .Q(S3), .preset(and_2_out), .reset(RST));  // open: Qn, en
  D_Flip_Flop d_ff_3 (.clk(CLK_out), .D(S3), .Q(S2), .preset(and_3_out), .reset(RST));  // open: Qn, en
  and and_3 (and_3_out, LOAD, D2);
  D_Flip_Flop d_ff_4 (.clk(CLK_out), .D(S2), .Q(S1), .preset(and_4_out), .reset(RST));  // open: Qn, en
  and and_4 (and_4_out, LOAD, D1);
  D_Flip_Flop d_ff_5 (.clk(CLK_out), .D(S1), .Q(S0), .preset(and_5_out), .reset(RST));  // open: Qn, en
  and and_5 (and_5_out, LOAD, D0);
endmodule
