// Logisim project Circuitos_395487.circ as structural Verilog: 7 circuits, main circuit Ex01
module Ex01 (
  input  Data,
  input  Clear,
  output S3,
  output S2,
  output S1,
  output S0
);

  wire CLK_out;

  Clock CLK (.out(CLK_out));
  D_Flip_Flop _3 (.clk(CLK_out), .D(S2), .Q(S3), .reset(Clear));  // open: Qn, preset, en
  D_Flip_Flop _2 (.clk(CLK_out), .D(S1), .Q(S2), .reset(Clear));  // open: Qn, preset, en
  D_Flip_Flop _1 (.clk(CLK_out), .D(S0), .Q(S1), .reset(Clear));  // open: Qn, preset, en
  D_Flip_Flop _0 (.clk(CLK_out), .D(Data), .Q(S0), .reset(Clear));  // open: Qn, preset, en

  // Notes on the sheet:
  //   Alvaro H A Rungue - 395487
endmodule

module Ex02 (
  input  Data,
  input  Clear,
  output S3,
  output S2,
  output S1,
  output S0
);

  wire CLK_out, or_1_out, or_2_out, or_3_out;

  Clock CLK (.out(CLK_out));
  D_Flip_Flop d_ff_1 (.clk(CLK_out), .D(or_1_out), .Q(S3), .reset(Clear));  // open: Qn, preset, en
  or or_1 (or_1_out, S2, Data);
  or or_2 (or_2_out, S1, Data);
  D_Flip_Flop d_ff_2 (.clk(CLK_out), .D(or_2_out), .Q(S2), .reset(Clear));  // open: Qn, preset, en
  D_Flip_Flop d_ff_3 (.clk(CLK_out), .D(or_3_out), .Q(S1), .reset(Clear));  // open: Qn, preset, en
  or or_3 (or_3_out, S0, Data);
  D_Flip_Flop d_ff_4 (.clk(CLK_out), .D(Data), .Q(S0), .reset(Clear));  // open: Qn, preset, en

  // Notes on the sheet:
  //   Alvaro H A Rungue - 395487
endmodule

module Ex03 (
  input  Data,
  input  Clear,
  output S3,
  output S2,
  output S1,
  output S0
);

  wire CLK_out;

  Clock CLK (.out(CLK_out));
  D_Flip_Flop d_ff_1 (.clk(CLK_out), .D(Data), .Q(S3), .reset(Clear));  // open: Qn, preset, en
  D_Flip_Flop d_ff_2 (.clk(CLK_out), .D(S3), .Q(S2), .reset(Clear));  // open: Qn, preset, en
  D_Flip_Flop d_ff_3 (.clk(CLK_out), .D(S2), .Q(S1), .reset(Clear));  // open: Qn, preset, en
  D_Flip_Flop d_ff_4 (.clk(CLK_out), .D(S1), .Q(S0), .reset(Clear));  // open: Qn, preset, en

  // Notes on the sheet:
  //   Alvaro H A Rungue - 395487
endmodule

module Ex04 (
  input  Data,
  input  Clear,
  output S3,
  output S2,
  output S1,
  output S0
);

  wire CLK_out, or_1_out;

  Clock CLK (.out(CLK_out));
  or or_1 (or_1_out, S3, Data);
  D_Flip_Flop d_ff_1 (.clk(CLK_out), .D(S2), .Q(S3), .reset(Clear));  // open: Qn, preset, en
  D_Flip_Flop d_ff_2 (.clk(CLK_out), .D(S1), .Q(S2), .reset(Clear));  // open: Qn, preset, en
  D_Flip_Flop d_ff_3 (.clk(CLK_out), .D(S0), .Q(S1), .reset(Clear));  // open: Qn, preset, en
  D_Flip_Flop d_ff_4 (.clk(CLK_out), .D(or_1_out), .Q(S0), .reset(Clear));  // open: Qn, preset, en

  // Notes on the sheet:
  //   Alvaro H A Rungue - 395487
endmodule

module Ex05 (
  input  RST,
  input  LOAD,
  input  D3,
  input  D2,
  input  D1,
  input  D0,
  output S3,
  output S2,
  output S1,
  output S0
);

  wire and_1_out, and_2_out, and_3_out, and_4_out, CLK_out;

  Clock CLK (.out(CLK_out));
  and and_1 (and_1_out, LOAD, D3);
  D_Flip_Flop d_ff_1 (.clk(CLK_out), .D(1'b0), .Q(S3), .preset(and_1_out), .reset(RST));  // open: Qn, en
  D_Flip_Flop d_ff_2 (.clk(CLK_out), .D(S3), .Q(S2), .preset(and_2_out), .reset(RST));  // open: Qn, en
  and and_2 (and_2_out, LOAD, D2);
  D_Flip_Flop d_ff_3 (.clk(CLK_out), .D(S2), .Q(S1), .preset(and_3_out), .reset(RST));  // open: Qn, en
  and and_3 (and_3_out, LOAD, D1);
  D_Flip_Flop d_ff_4 (.clk(CLK_out), .D(S1), .Q(S0), .preset(and_4_out), .reset(RST));  // open: Qn, en
  and and_4 (and_4_out, LOAD, D0);

  // Notes on the sheet:
  //   Alvaro H A Rungue - 395487
endmodule

module Ex06 (
  input  Data,
  input  Clear,
  output out_3,
  output out_4,
  output out_5,
  output out_6
);

  wire clock_1_out, or_1_out, or_2_out, or_3_out, or_4_out;

  Clock clock_1 (.out(clock_1_out));
  D_Flip_Flop d_ff_1 (.clk(clock_1_out), .D(or_1_out), .Q(out_3), .reset(Clear));  // open: Qn, preset, en
  or or_1 (or_1_out, out_6, Data);
  or or_2 (or_2_out, out_3, Data);
  D_Flip_Flop d_ff_2 (.clk(clock_1_out), .D(or_2_out), .Q(out_4), .reset(Clear));  // open: Qn, preset, en
  or or_3 (or_3_out, out_4, Data);
  D_Flip_Flop d_ff_3 (.clk(clock_1_out), .D(or_3_out), .Q(out_5), .reset(Clear));  // open: Qn, preset, en
  or or_4 (or_4_out, out_5, Data);
  D_Flip_Flop d_ff_4 (.clk(clock_1_out), .D(or_4_out), .Q(out_6), .reset(Clear));  // open: Qn, preset, en

  // Notes on the sheet:
  //   Alvaro H A Rungue - 395487
endmodule

module Ex07 (
  input  Data,
  input  Clear,
  output out_3,
  output out_4,
  output out_5,
  output out_6
);

  wire clock_1_out, d_ff_4_qn, or_1_out, or_2_out, or_3_out, or_4_out;

  Clock clock_1 (.out(clock_1_out));
  D_Flip_Flop d_ff_1 (.clk(clock_1_out), .D(or_1_out), .Q(out_3), .reset(Clear));  // open: Qn, preset, en
  or or_1 (or_1_out, d_ff_4_qn, Data);
  or or_2 (or_2_out, out_3, Data);
  D_Flip_Flop d_ff_2 (.clk(clock_1_out), .D(or_2_out), .Q(out_4), .reset(Clear));  // open: Qn, preset, en
  or or_3 (or_3_out, out_4, Data);
  D_Flip_Flop d_ff_3 (.clk(clock_1_out), .D(or_3_out), .Q(out_5), .reset(Clear));  // open: Qn, preset, en
  D_Flip_Flop d_ff_4 (.clk(clock_1_out), .D(or_4_out), .Q(out_6), .Qn(d_ff_4_qn), .reset(Clear));  // open: preset, en
  or or_4 (or_4_out, out_5, Data);

  // Notes on the sheet:
  //   Alvaro H A Rungue - 395487
endmodule
