// Logisim project Exercicio0081.circ as structural Verilog: 1 circuit, main circuit main
module main (
  input  D,
  input  clr,
  output a,
  output b,
  output c,
  output d_2
);

  wire CLK_out;

  Clock CLK (.out(CLK_out));
  D_Flip_Flop d_ff_1 (.clk(CLK_out), .D(b), .Q(a), .reset(clr));  // open: Qn, preset, en
  D_Flip_Flop d_ff_2 (.clk(CLK_out), .D(c), .Q(b), .reset(clr));  // open: Qn, preset, en
  D_Flip_Flop d_ff_3 (.clk(CLK_out), .D(d_2), .Q(c), .reset(clr));  // open: Qn, preset, en
  D_Flip_Flop d_ff_4 (.clk(CLK_out), .D(D), .Q(d_2), .reset(clr));  // open: Qn, preset, en
endmodule
