// Logisim project Exercicio0082.circ as structural Verilog: 1 circuit, main circuit main
module main (
  input  Input,
  input  CLR,
  input  in_3,
  input  in_4,
  input  in_5,
  input  in_6,
  output a,
  output b,
  output c,
  output d
);

  wire CLK_out;

  Clock CLK (.out(CLK_out));
  D_Flip_Flop f1 (.clk(CLK_out), .D(b), .Q(a), .preset(in_3), .reset(CLR));  // open: Qn, en
  D_Flip_Flop f2 (.clk(CLK_out), .D(c), .Q(b), .preset(in_4), .reset(CLR));  // open: Qn, en
  D_Flip_Flop f3 (.clk(CLK_out), .D(d), .Q(c), .preset(in_5), .reset(CLR));  // open: Qn, en
  D_Flip_Flop f4 (.clk(CLK_out), .D(Input), .Q(d), .preset(in_6), .reset(CLR));  // open: Qn, en
endmodule
