// Logisim project Exercicio0087.circ as structural Verilog: 1 circuit, main circuit main
module main (
  input  \input ,
  input  clear,
  input  in_3,
  input  in_4,
  input  in_5,
  input  in_6
);

  wire clk_out, d_ff_1_q, d_ff_2_q, d_ff_3_q, d_ff_4_qn, or_1_out;

  Clock clk (.out(clk_out));
  or or_1 (or_1_out, d_ff_4_qn, \input );
  D_Flip_Flop d_ff_1 (.clk(clk_out), .D(or_1_out), .Q(d_ff_1_q), .preset(in_3), .reset(clear));  // open: Qn, en
  D_Flip_Flop d_ff_2 (.clk(clk_out), .D(d_ff_1_q), .Q(d_ff_2_q), .preset(in_4), .reset(clear));  // open: Qn, en
  D_Flip_Flop d_ff_3 (.clk(clk_out), .D(d_ff_2_q), .Q(d_ff_3_q), .preset(in_5), .reset(clear));  // open: Qn, en
  D_Flip_Flop d_ff_4 (.clk(clk_out), .D(d_ff_3_q), .Qn(d_ff_4_qn), .preset(in_6), .reset(clear));  // open: Q, en

  // Notes on the sheet:
  //   Preset
endmodule
