// Logisim project Exercicio002.circ as structural Verilog: 1 circuit, main circuit main
module main (
  input  data,
  input  CLR,
  input  preset,
  output a,
  output b,
  output c,
  output d
);

  wire CLK_out;

  Clock CLK (.out(CLK_out));
  D_Flip_Flop d_ff_1 (.clk(CLK_out), .D(b), .Q(a), .preset(preset), .reset(CLR));  // open: Qn, en
  D_Flip_Flop d_ff_2 (.clk(CLK_out), .D(c), .Q(b), .preset(preset), .reset(CLR));  // open: Qn, en
  D_Flip_Flop d_ff_3 (.clk(CLK_out), .D(d), .Q(c), .preset(preset), .reset(CLR));  // open: Qn, en
  D_Flip_Flop d_ff_4 (.clk(CLK_out), .D(data), .Q(d), .preset(preset), .reset(CLR));  // open: Qn, en
endmodule
