// Logisim project Exercicio004.circ as structural Verilog: 1 circuit, main circuit main
module main (
  input  \input ,
  input  CLR,
  output a,
  output b,
  output c
);

  wire CLK_out, or_1_out;

  Clock CLK (.out(CLK_out));
  or or_1 (or_1_out, a, \input );
  D_Flip_Flop d_ff_1 (.clk(CLK_out), .D(b), .Q(a), .reset(CLR));  // open: Qn, preset, en
  D_Flip_Flop d_ff_2 (.clk(CLK_out), .D(c), .Q(b), .reset(CLR));  // open: Qn, preset, en
  D_Flip_Flop d_ff_3 (.clk(CLK_out), .D(or_1_out), .Q(c), .reset(CLR));  // open: Qn, preset, en
endmodule
