// Logisim project Exercicio01 Shift register (left).circ as structural Verilog: 1 circuit, main circuit main
module main (
  input  DATA,
  input  CLR,
  output A,
  output B,
  output C,
  output D
);

  wire CLK_out;

  Clock CLK (.out(CLK_out));
  D_Flip_Flop d_ff_1 (.clk(CLK_out), .D(B), .Q(A), .reset(CLR));  // open: Qn, preset, en
  D_Flip_Flop d_ff_2 (.clk(CLK_out), .D(C), .Q(B), .reset(CLR));  // open: Qn, preset, en
  D_Flip_Flop d_ff_3 (.clk(CLK_out), .D(D), .Q(C), .reset(CLR));  // open: Qn, preset, en
  D_Flip_Flop d_ff_4 (.clk(CLK_out), .D(DATA), .Q(D), .reset(CLR));  // open: Qn, preset, en
endmodule
