// Logisim project Exercicio02 Shift register  (left) com anel torcido.circ as structural Verilog: 1 circuit, main circuit main
module main (
  input  CLR,
  input  DATA,
  output A,
  output B,
  output C,
  output D
);

  wire CLK_out, or_1_out, or_2_out, or_3_out;

  Clock CLK (.out(CLK_out));
  D_Flip_Flop d_ff_1 (.clk(CLK_out), .D(or_1_out), .Q(A), .reset(CLR));  // open: Qn, preset, en
  or or_1 (or_1_out, DATA, B);
  D_Flip_Flop d_ff_2 (.clk(CLK_out), .D(or_2_out), .Q(B), .reset(CLR));  // open: Qn, preset, en
  or or_2 (or_2_out, DATA, C);
  or or_3 (or_3_out, DATA, D);
  D_Flip_Flop d_ff_3 (.clk(CLK_out), .D(or_3_out), .Q(C), .reset(CLR));  // open: Qn, preset, en
  D_Flip_Flop d_ff_4 (.clk(CLK_out), .D(DATA), .Q(D), .reset(CLR));  // open: Qn, preset, en
endmodule
