// Logisim project Exercicio04 Shift register  (left) com anel torcido.circ as structural Verilog: 1 circuit, main circuit main
module main (
  input  DATA,
  input  CLR,
  output A,
  output B,
  output C,
  output D,
  output D_2
);

  wire clock_1_out, or_1_out;

  Clock clock_1 (.out(clock_1_out));
  or or_1 (or_1_out, A, DATA);
  D_Flip_Flop d_ff_1 (.clk(clock_1_out), .D(B), .Q(A), .reset(CLR));  // open: Qn, preset, en
  D_Flip_Flop d_ff_2 (.clk(clock_1_out), .D(C), .Q(B), .reset(CLR));  // open: Qn, preset, en
  D_Flip_Flop d_ff_3 (.clk(clock_1_out), .D(D), .Q(C), .reset(CLR));  // open: Qn, preset, en
  D_Flip_Flop d_ff_4 (.clk(clock_1_out), .D(or_1_out), .Q(D), .reset(CLR));  // open: Qn, preset, en
endmodule
