// Logisim project Extras-01.circ as structural Verilog: 1 circuit, main circuit main
module main (
  input  CRL,
  input  DATA,
  output A,
  output B,
  output C,
  output D
);

  wire CLK_out, or_1_out, or_2_out, or_3_out, or_4_out;

  Clock CLK (.out(CLK_out));
  or or_1 (or_1_out, D, DATA);
  D_Flip_Flop d_ff_1 (.clk(CLK_out), .D(or_1_out), .Q(A), .reset(CRL));  // open: Qn, preset, en
  D_Flip_Flop d_ff_2 (.clk(CLK_out), .D(or_2_out), .Q(B), .reset(CRL));  // open: Qn, preset, en
  or or_2 (or_2_out, A, DATA);
  or or_3 (or_3_out, B, DATA);
  D_Flip_Flop d_ff_3 (.clk(CLK_out), .D(or_3_out), .Q(C), .reset(CRL));  // open: Qn, preset, en
  or or_4 (or_4_out, C, DATA);
  D_Flip_Flop d_ff_4 (.clk(CLK_out), .D(or_4_out), .Q(D), .reset(CRL));  // open: Qn, preset, en
endmodule
