// Logisim project exercicio03 Shift register   (rigth).circ as structural Verilog: 1 circuit, main circuit main
module main (
  input  DATA,
  input  CLR,
  output A,
  output B,
  output C,
  output D
);

  wire CLK_out, or_1_out;

  Clock CLK (.out(CLK_out));
  D_Flip_Flop d_ff_1 (.clk(CLK_out), .D(or_1_out), .Q(A), .reset(CLR));  // open: Qn, preset, en
  or or_1 (or_1_out, D, DATA);
  D_Flip_Flop d_ff_2 (.clk(CLK_out), .D(A), .Q(B), .reset(CLR));  // open: Qn, preset, en
  D_Flip_Flop d_ff_3 (.clk(CLK_out), .D(B), .Q(C), .reset(CLR));  // open: Qn, preset, en
  D_Flip_Flop d_ff_4 (.clk(CLK_out), .D(C), .Q(D), .reset(CLR));  // open: Qn, preset, en
endmodule
