// Logisim project Exercicio02.circ as structural Verilog: 1 circuit, main circuit main
module main (
  input  in_1,
  input  in_2,
  output out_3,
  output out_4,
  output out_5,
  output out_6
);

  wire clock_1_out;

  Clock clock_1 (.out(clock_1_out));
  D_Flip_Flop d_ff_1 (.clk(clock_1_out), .D(out_4), .Q(out_3), .preset(in_1), .reset(in_2));  // open: Qn, en
  D_Flip_Flop d_ff_2 (.clk(clock_1_out), .D(out_5), .Q(out_4), .preset(in_1), .reset(in_2));  // open: Qn, en
  D_Flip_Flop d_ff_3 (.clk(clock_1_out), .D(out_6), .Q(out_5), .preset(in_1), .reset(in_2));  // open: Qn, en
  D_Flip_Flop d_ff_4 (.clk(clock_1_out), .D(in_1), .Q(out_6), .preset(in_1), .reset(in_2));  // open: Qn, en

  // Notes on the sheet:
  //   Filipe Viana de Miranda - 446415
endmodule
