// Logisim project Exercicio02.circ as structural Verilog: 1 circuit, main circuit main
module main (
  input  CLK,
  input  IN,
  input  CLR,
  output out_4,
  output out_5,
  output out_6,
  output out_7
);

  D_Flip_Flop d_ff_1 (.clk(CLK), .D(out_5), .Q(out_4), .preset(IN), .reset(CLR));  // open: Qn, en
  D_Flip_Flop d_ff_2 (.clk(CLK), .D(out_6), .Q(out_5), .preset(IN), .reset(CLR));  // open: Qn, en
  D_Flip_Flop d_ff_3 (.clk(CLK), .D(out_7), .Q(out_6), .preset(IN), .reset(CLR));  // open: Qn, en
  D_Flip_Flop d_ff_4 (.clk(CLK), .D(IN), .Q(out_7), .preset(IN), .reset(CLR));  // open: Qn, en
endmodule
