// Logisim project Exercicio04.circ as structural Verilog: 1 circuit, main circuit main
module main (
  input  IN,
  input  CLR,
  output out_3,
  output out_4,
  output out_5,
  output out_6
);

  wire CLK_out, or_1_out;

  Clock CLK (.out(CLK_out));
  or or_1 (or_1_out, out_3, IN);
  D_Flip_Flop d_ff_1 (.clk(CLK_out), .D(out_4), .Q(out_3), .reset(CLR));  // open: Qn, preset, en
  D_Flip_Flop d_ff_2 (.clk(CLK_out), .D(out_5), .Q(out_4), .reset(CLR));  // open: Qn, preset, en
  D_Flip_Flop d_ff_3 (.clk(CLK_out), .D(out_6), .Q(out_5), .reset(CLR));  // open: Qn, preset, en
  D_Flip_Flop d_ff_4 (.clk(CLK_out), .D(or_1_out), .Q(out_6), .reset(CLR));  // open: Qn, preset, en
endmodule
