// Logisim project Exercicio05.circ as structural Verilog: 1 circuit, main circuit main
module main (
  input  CLR,
  input  LD,
  input  a3,
  input  a2,
  input  a1,
  input  a0,
  output s3,
  output s2,
  output s1,
  output s0
);

  wire and_1_out, and_2_out, and_3_out, and_4_out, CLK_out;

  Clock CLK (.out(CLK_out));
  and and_1 (and_1_out, LD, a3);
  D_Flip_Flop d_ff_1 (.clk(CLK_out), .D(1'b0), .Q(s3), .preset(and_1_out), .reset(CLR));  // open: Qn, en
  and and_2 (and_2_out, LD, a2);
  D_Flip_Flop d_ff_2 (.clk(CLK_out), .D(s3), .Q(s2), .preset(and_2_out), .reset(CLR));  // open: Qn, en
  and and_3 (and_3_out, LD, a1);
  D_Flip_Flop d_ff_3 (.clk(CLK_out), .D(s2), .Q(s1), .preset(and_3_out), .reset(CLR));  // open: Qn, en
  and and_4 (and_4_out, LD, a0);
  D_Flip_Flop d_ff_4 (.clk(CLK_out), .D(s1), .Q(s0), .preset(and_4_out), .reset(CLR));  // open: Qn, en
endmodule
