// Logisim project Exercicio0083.circ as structural Verilog: 1 circuit, main circuit main
module main (
  input  \input ,
  input  clear
);

  wire clk_out, d_ff_1_q, d_ff_2_q, d_ff_3_q, d_ff_4_q, or_1_out;

  Clock clk (.out(clk_out));
  or or_1 (or_1_out, \input , d_ff_4_q);
  D_Flip_Flop d_ff_1 (.clk(clk_out), .D(or_1_out), .Q(d_ff_1_q), .reset(clear));  // open: Qn, preset, en
  D_Flip_Flop d_ff_2 (.clk(clk_out), .D(d_ff_3_q), .Q(d_ff_2_q), .reset(clear));  // open: Qn, preset, en
  D_Flip_Flop d_ff_3 (.clk(clk_out), .D(d_ff_1_q), .Q(d_ff_3_q), .reset(clear));  // open: Qn, preset, en
  D_Flip_Flop d_ff_4 (.clk(clk_out), .D(d_ff_2_q), .Q(d_ff_4_q), .reset(clear));  // open: Qn, preset, en
endmodule
