// Logisim project Exercicio0084.circ as structural Verilog: 1 circuit, main circuit main
module main (
  input  clear,
  input  \input 
);

  wire clock_1_out, d_ff_1_qn, d_ff_2_q, d_ff_3_q, d_ff_4_q, or_1_out;

  Clock clock_1 (.out(clock_1_out));
  or or_1 (or_1_out, \input , d_ff_1_qn);
  D_Flip_Flop d_ff_1 (.clk(clock_1_out), .D(d_ff_2_q), .Qn(d_ff_1_qn), .reset(clear));  // open: Q, preset, en
  D_Flip_Flop d_ff_2 (.clk(clock_1_out), .D(d_ff_3_q), .Q(d_ff_2_q), .reset(clear));  // open: Qn, preset, en
  D_Flip_Flop d_ff_3 (.clk(clock_1_out), .D(d_ff_4_q), .Q(d_ff_3_q), .reset(clear));  // open: Qn, preset, en
  D_Flip_Flop d_ff_4 (.clk(clock_1_out), .D(or_1_out), .Q(d_ff_4_q), .reset(clear));  // open: Qn, preset, en
endmodule
