// Logisim project Exercicio0085.circ as structural Verilog: 1 circuit, main circuit main
module main (
  input  clear,
  input  Load,
  input  in_3,
  input  in_4,
  input  in_5,
  input  in_6,
  output a,
  output b,
  output c,
  output d
);

  wire and_1_out, and_2_out, and_3_out, and_4_out, clock_1_out;

  Clock clock_1 (.out(clock_1_out));
  D_Flip_Flop d_ff_1 (.clk(clock_1_out), .D(1'b0), .Q(a), .preset(and_1_out), .reset(clear));  // open: Qn, en
  and and_1 (and_1_out, in_3, Load);
  and and_2 (and_2_out, in_4, Load);
  D_Flip_Flop d_ff_2 (.clk(clock_1_out), .D(a), .Q(b), .preset(and_2_out), .reset(clear));  // open: Qn, en
  and and_3 (and_3_out, in_5, Load);
  D_Flip_Flop d_ff_3 (.clk(clock_1_out), .D(b), .Q(c), .preset(and_3_out), .reset(clear));  // open: Qn, en
  and and_4 (and_4_out, in_6, Load);
  D_Flip_Flop d_ff_4 (.clk(clock_1_out), .D(c), .Q(d), .preset(and_4_out), .reset(clear));  // open: Qn, en
endmodule
