// Logisim project Exercicio001.circ as structural Verilog: 1 circuit, main circuit main
module main (
  input  data,
  input  CLR,
  output QA,
  output QB,
  output QC,
  output QD
);

  wire CLK_out;

  Clock CLK (.out(CLK_out));
  D_Flip_Flop A (.clk(CLK_out), .D(QB), .Q(QA), .preset(1'b1), .reset(CLR));  // open: Qn, en
  D_Flip_Flop B (.clk(CLK_out), .D(QC), .Q(QB), .reset(CLR));  // open: Qn, preset, en
  D_Flip_Flop C (.clk(CLK_out), .D(QD), .Q(QC), .reset(CLR));  // open: Qn, preset, en
  D_Flip_Flop D (.clk(CLK_out), .D(data), .Q(QD), .reset(CLR));  // open: Qn, preset, en

  // Notes on the sheet:
  //   clk
  //   qb
  //   clk
  //   qc
  //   clk
  //   qd
  //   As saidas dos flip flops posteriores alimentam a entrada D dos anteriores, nesse momento ocorre a passagem do sinal
  //   clk
  //   data
endmodule
