// Logisim project Exercicio002.circ as structural Verilog: 1 circuit, main circuit main
module main (
  input  data,
  input  carga_Inicial,
  input  Celar,
  output a,
  output b,
  output c,
  output d
);

  wire Clock_out;

  Clock Clock (.out(Clock_out));
  D_Flip_Flop u_A (.clk(Clock_out), .D(b), .Q(a), .preset(carga_Inicial), .reset(Celar));  // open: Qn, en
  D_Flip_Flop u_B (.clk(Clock_out), .D(c), .Q(b), .preset(carga_Inicial), .reset(Celar));  // open: Qn, en
  D_Flip_Flop u_C (.clk(Clock_out), .D(d), .Q(c), .preset(carga_Inicial), .reset(Celar));  // open: Qn, en
  D_Flip_Flop u_D (.clk(Clock_out), .D(data), .Q(d), .preset(carga_Inicial), .reset(Celar));  // open: Qn, en
endmodule
