// Logisim project Exercicio003.circ as structural Verilog: 1 circuit, main circuit main
module main (
  input  data,
  input  Clear,
  output a,
  output b,
  output c,
  output d
);

  wire Clock_out, or_1_out;

  Clock Clock (.out(Clock_out));
  or or_1 (or_1_out, d, data);
  D_Flip_Flop u_A (.clk(Clock_out), .D(or_1_out), .Q(a), .preset(1'b1), .reset(Clear));  // open: Qn, en
  D_Flip_Flop u_B (.clk(Clock_out), .D(a), .Q(b), .reset(Clear));  // open: Qn, preset, en
  D_Flip_Flop u_C (.clk(Clock_out), .D(b), .Q(c), .reset(Clear));  // open: Qn, preset, en
  D_Flip_Flop u_D (.clk(Clock_out), .D(c), .Q(d), .reset(Clear));  // open: Qn, preset, en
endmodule
