// Logisim project Exercicio04.circ as structural Verilog: 1 circuit, main circuit main
module main (
  input  data,
  input  clear,
  output [3:0] saida
);

  wire A_qn, clock_out, O_out;

  Clock clock (.out(clock_out));
  or O (O_out, A_qn, data);
  D_Flip_Flop A (.clk(clock_out), .D(saida[2]), .Q(saida[3]), .Qn(A_qn), .reset(clear));  // open: preset, en
  D_Flip_Flop B (.clk(clock_out), .D(saida[1]), .Q(saida[2]), .reset(clear));  // open: Qn, preset, en
  D_Flip_Flop C (.clk(clock_out), .D(saida[0]), .Q(saida[1]), .reset(clear));  // open: Qn, preset, en
  D_Flip_Flop D (.clk(clock_out), .D(O_out), .Q(saida[0]), .reset(clear));  // open: Qn, preset, en

  // Notes on the sheet:
  //   qNotA
  //   x0
  //   qb
  //   ANEL TORCIDO: a saida do A que retroalimenta o circuito e invertida
  //   qc
  //   qd
  //   x0
endmodule
