// Logisim project Exercicio05.circ as structural Verilog: 1 circuit, main circuit main
module main (
  input  Clear,
  input  LD,
  input  [3:0] Entrada_paralela,
  output [3:0] Saida_Serial
);

  wire Clock_out, E_out, F_out, G_out, H_out;

  Clock Clock (.out(Clock_out));
  D_Flip_Flop A (.clk(Clock_out), .D(1'b0), .Q(Saida_Serial[3]), .preset(E_out), .reset(Clear));  // open: Qn, en
  and E (E_out, LD, Entrada_paralela[3]);
  D_Flip_Flop B (
    .clk(Clock_out), .D(Saida_Serial[3]), .Q(Saida_Serial[2]), .preset(F_out), .reset(Clear));  // open: Qn, en
  and F (F_out, LD, Entrada_paralela[2]);
  D_Flip_Flop C (
    .clk(Clock_out), .D(Saida_Serial[2]), .Q(Saida_Serial[1]), .preset(G_out), .reset(Clear));  // open: Qn, en
  and G (G_out, LD, Entrada_paralela[1]);
  and H (H_out, LD, Entrada_paralela[0]);
  D_Flip_Flop D (
    .clk(Clock_out), .D(Saida_Serial[1]), .Q(Saida_Serial[0]), .preset(H_out), .reset(Clear));  // open: Qn, en

  // Notes on the sheet:
  //   x3
  //   d3
  //    <= ordem da entrada: d3 d2 d1 d0
  //   qa
  //   x2
  //   d2
  //   ordem da saida: a b c d =>
  //   qb
  //   x1
  //   d1
  //   qc
  //   x0
  //   d0
endmodule
