// Logisim project Exercicio06.circ as structural Verilog: 1 circuit, main circuit main
module main (
  input  data,
  input  Clear,
  input  Caraga_Inicial,
  output [3:0] saidas
);

  wire Clock_out, O_out;

  Clock Clock (.out(Clock_out));
  or O (O_out, saidas[0], data);
  D_Flip_Flop A (.clk(Clock_out), .D(O_out), .Q(saidas[3]), .preset(Caraga_Inicial), .reset(Clear));  // open: Qn, en
  D_Flip_Flop B (
    .clk(Clock_out), .D(saidas[3]), .Q(saidas[2]), .preset(Caraga_Inicial), .reset(Clear));  // open: Qn, en
  D_Flip_Flop C (
    .clk(Clock_out), .D(saidas[2]), .Q(saidas[1]), .preset(Caraga_Inicial), .reset(Clear));  // open: Qn, en
  D_Flip_Flop D (
    .clk(Clock_out), .D(saidas[1]), .Q(saidas[0]), .preset(Caraga_Inicial), .reset(Clear));  // open: Qn, en

  // Notes on the sheet:
  //   qd
  //   x0
  //   qa
  //   qb
  //   qc
endmodule
