// Logisim project Exercicio07.circ as structural Verilog: 1 circuit, main circuit main
module main (
  input  Data,
  input  Clear,
  input  Carga_Inicial,
  output [3:0] Saidas
);

  wire Clock_out, D_qn, O_out;

  Clock Clock (.out(Clock_out));
  D_Flip_Flop A (.clk(Clock_out), .D(O_out), .Q(Saidas[3]), .preset(Carga_Inicial), .reset(Clear));  // open: Qn, en
  or O (O_out, Data, D_qn);
  D_Flip_Flop B (.clk(Clock_out), .D(Saidas[3]), .Q(Saidas[2]), .preset(Carga_Inicial), .reset(Clear));  // open: Qn, en
  D_Flip_Flop C (.clk(Clock_out), .D(Saidas[2]), .Q(Saidas[1]), .preset(Carga_Inicial), .reset(Clear));  // open: Qn, en
  D_Flip_Flop D (
    .clk(Clock_out), .D(Saidas[1]), .Q(Saidas[0]), .Qn(D_qn), .preset(Carga_Inicial), .reset(Clear));  // open: en

  // Notes on the sheet:
  //   qNotD
  //   x0
  //   qa
  //   qb
  //   qd
  //   qc
endmodule
