// Logisim project Exercicio02.circ as structural Verilog: 1 circuit, main circuit main
module main (
  input  in_1,
  input  in_2,
  input  in_3,
  output out_4,
  output out_5,
  output out_6,
  output out_7
);

  D_Flip_Flop d_ff_1 (.clk(in_1), .D(out_5), .Q(out_4), .preset(in_2), .reset(in_3));  // open: Qn, en
  D_Flip_Flop d_ff_2 (.clk(in_1), .D(out_6), .Q(out_5), .preset(in_2), .reset(in_3));  // open: Qn, en
  D_Flip_Flop d_ff_3 (.clk(in_1), .D(out_7), .Q(out_6), .preset(in_2), .reset(in_3));  // open: Qn, en
  D_Flip_Flop d_ff_4 (.clk(in_1), .D(in_2), .Q(out_7), .preset(in_2), .reset(in_3));  // open: Qn, en
endmodule
