// Logisim project Exercicio03.circ as structural Verilog: 1 circuit, main circuit main
module main (
  input  pulse,
  input  CLR,
  output a,
  output b,
  output c,
  output d
);

  wire CLK_out, or_1_out;

  Clock CLK (.out(CLK_out));
  or or_1 (or_1_out, d, pulse);
  D_Flip_Flop u_A (.clk(CLK_out), .D(or_1_out), .Q(a), .reset(CLR));  // open: Qn, preset, en
  D_Flip_Flop u_B (.clk(CLK_out), .D(a), .Q(b), .reset(CLR));  // open: Qn, preset, en
  D_Flip_Flop u_C (.clk(CLK_out), .D(b), .Q(c), .reset(CLR));  // open: Qn, preset, en
  D_Flip_Flop d_ff_1 (.clk(CLK_out), .D(c), .Q(d), .reset(CLR));  // open: Qn, preset, en

  // Notes on the sheet:
  //   D
endmodule
