// Logisim project Exercicio04.circ as structural Verilog: 1 circuit, main circuit main
module main (
  input  d,
  input  CLR,
  output a,
  output b,
  output c,
  output d_2
);

  wire A_qn, CLK_out, or_1_out;

  Clock CLK (.out(CLK_out));
  or or_1 (or_1_out, d, A_qn);
  D_Flip_Flop u_A (.clk(CLK_out), .D(b), .Q(a), .Qn(A_qn), .reset(CLR));  // open: preset, en
  D_Flip_Flop u_B (.clk(CLK_out), .D(c), .Q(b), .reset(CLR));  // open: Qn, preset, en
  D_Flip_Flop u_C (.clk(CLK_out), .D(d_2), .Q(c), .reset(CLR));  // open: Qn, preset, en
  D_Flip_Flop d_ff_1 (.clk(CLK_out), .D(or_1_out), .Q(d_2), .reset(CLR));  // open: Qn, preset, en

  // Notes on the sheet:
  //   D
endmodule
