// Logisim project Exercicio1.circ as structural Verilog: 3 circuits, main circuit Deslocador Esquerda
// SHL
module Deslocador_Esquerda (
  input  Input,
  input  CLR
);

  wire CLK_out, d_ff_1_q, d_ff_2_q, d_ff_3_q, d_ff_4_q;

  Clock CLK (.out(CLK_out));
  // Probe on d_ff_1_q
  D_Flip_Flop d_ff_1 (.clk(CLK_out), .D(d_ff_2_q), .Q(d_ff_1_q), .reset(CLR));  // open: Qn, preset, en
  // Probe on d_ff_2_q
  D_Flip_Flop d_ff_2 (.clk(CLK_out), .D(d_ff_3_q), .Q(d_ff_2_q), .reset(CLR));  // open: Qn, preset, en
  // Probe on d_ff_3_q
  D_Flip_Flop d_ff_3 (.clk(CLK_out), .D(d_ff_4_q), .Q(d_ff_3_q), .reset(CLR));  // open: Qn, preset, en
  D_Flip_Flop d_ff_4 (.clk(CLK_out), .D(Input), .Q(d_ff_4_q), .reset(CLR));  // open: Qn, preset, en
  // Probe on d_ff_4_q
endmodule

// SHR
module Deslocador_Direita (
  input  Input,
  input  CLR
);

  wire CLK_out, d_ff_1_q, d_ff_2_q, d_ff_3_q, d_ff_4_q;

  Clock CLK (.out(CLK_out));
  // Probe on d_ff_1_q
  D_Flip_Flop d_ff_1 (.clk(CLK_out), .D(Input), .Q(d_ff_1_q), .reset(CLR));  // open: Qn, preset, en
  // Probe on d_ff_2_q
  D_Flip_Flop d_ff_2 (.clk(CLK_out), .D(d_ff_1_q), .Q(d_ff_2_q), .reset(CLR));  // open: Qn, preset, en
  // Probe on d_ff_3_q
  D_Flip_Flop d_ff_3 (.clk(CLK_out), .D(d_ff_2_q), .Q(d_ff_3_q), .reset(CLR));  // open: Qn, preset, en
  D_Flip_Flop d_ff_4 (.clk(CLK_out), .D(d_ff_3_q), .Q(d_ff_4_q), .reset(CLR));  // open: Qn, preset, en
  // Probe on d_ff_4_q
endmodule

module Paralelo_to_Serie (
  input  CLR,
  input  LD,
  input  D3,
  input  D2,
  input  D1,
  input  D0
);

  wire and_1_out, and_2_out, and_3_out, and_4_out, CLK_out, d_ff_1_q, d_ff_2_q, d_ff_3_q, d_ff_4_q;

  Clock CLK (.out(CLK_out));
  // Probe on d_ff_1_q
  D_Flip_Flop d_ff_1 (.clk(CLK_out), .Q(d_ff_1_q), .preset(and_1_out), .reset(CLR));  // open: D, Qn, en
  and and_1 (and_1_out, LD, D3);
  // Probe on d_ff_2_q
  D_Flip_Flop d_ff_2 (.clk(CLK_out), .D(d_ff_1_q), .Q(d_ff_2_q), .preset(and_2_out), .reset(CLR));  // open: Qn, en
  and and_2 (and_2_out, LD, D2);
  // Probe on d_ff_3_q
  D_Flip_Flop d_ff_3 (.clk(CLK_out), .D(d_ff_2_q), .Q(d_ff_3_q), .preset(and_3_out), .reset(CLR));  // open: Qn, en
  and and_3 (and_3_out, LD, D1);
  // Probe on d_ff_4_q
  D_Flip_Flop d_ff_4 (.clk(CLK_out), .D(d_ff_3_q), .Q(d_ff_4_q), .preset(and_4_out), .reset(CLR));  // open: Qn, en
  and and_4 (and_4_out, LD, D0);
endmodule
