// Logisim project Rotate Register (Left) .circ as structural Verilog: 1 circuit, main circuit main
module main (
  input  data,
  input  CLR,
  output a,
  output b,
  output c,
  output d
);

  wire Clock_out, or_1_out;

  Clock Clock (.out(Clock_out));
  or or_1 (or_1_out, a, data);
  D_Flip_Flop d_ff_1 (.clk(Clock_out), .D(b), .Q(a), .reset(CLR));  // open: Qn, preset, en
  D_Flip_Flop d_ff_2 (.clk(Clock_out), .D(c), .Q(b), .reset(CLR));  // open: Qn, preset, en
  D_Flip_Flop d_ff_3 (.clk(Clock_out), .D(d), .Q(c), .reset(CLR));  // open: Qn, preset, en
  D_Flip_Flop d_ff_4 (.clk(Clock_out), .D(or_1_out), .Q(d), .reset(CLR));  // open: Qn, preset, en
endmodule
