// Logisim project (Left) Shift Register.circ as structural Verilog: 1 circuit, main circuit main
module main (
  input  CLK,
  input  data,
  input  CLR,
  output a,
  output b,
  output c,
  output d
);

  D_Flip_Flop d_ff_1 (.clk(CLK), .D(b), .Q(a), .reset(CLR));  // open: Qn, preset, en
  D_Flip_Flop d_ff_2 (.clk(CLK), .D(c), .Q(b), .reset(CLR));  // open: Qn, preset, en
  D_Flip_Flop d_ff_3 (.clk(CLK), .D(d), .Q(c), .reset(CLR));  // open: Qn, preset, en
  D_Flip_Flop d_ff_4 (.clk(CLK), .D(data), .Q(d), .reset(CLR));  // open: Qn, preset, en
endmodule
