// Logisim project Rotate Register (Right) .circ as structural Verilog: 1 circuit, main circuit main
module main (
  input  data,
  input  CLR,
  output a,
  output b,
  output c,
  output d
);

  wire clock_1_out, or_1_out;

  // Probe on d
  Clock clock_1 (.out(clock_1_out));
  or or_1 (or_1_out, d, data);
  D_Flip_Flop d_ff_1 (.clk(clock_1_out), .D(or_1_out), .Q(a), .reset(CLR));  // open: Qn, preset, en
  D_Flip_Flop d_ff_2 (.clk(clock_1_out), .D(a), .Q(b), .reset(CLR));  // open: Qn, preset, en
  D_Flip_Flop d_ff_3 (.clk(clock_1_out), .D(b), .Q(c), .reset(CLR));  // open: Qn, preset, en
  D_Flip_Flop d_ff_4 (.clk(clock_1_out), .D(c), .Q(d), .reset(CLR));  // open: Qn, preset, en
endmodule
