// Logisim project Exercicio01.circ as structural Verilog: 1 circuit, main circuit main
module main (
  input  in_1,
  input  in_2,
  input  in_3,
  output out_4,
  output out_5,
  output out_6,
  output out_7,
  output out_8
);

  wire clock_1_out;

  Clock clock_1 (.out(clock_1_out));
  J_K_Flip_Flop j_k_ff_1 (
    .J(in_1), .clk(clock_1_out), .K(in_1), .Q(out_8), .preset(in_3), .reset(in_2));  // open: Qn, en
  J_K_Flip_Flop j_k_ff_2 (.J(out_8), .clk(out_8), .K(out_8), .Q(out_7), .preset(in_3), .reset(in_2));  // open: Qn, en
  J_K_Flip_Flop j_k_ff_3 (.J(out_7), .clk(out_7), .K(out_7), .Q(out_6), .preset(in_3), .reset(in_2));  // open: Qn, en
  J_K_Flip_Flop j_k_ff_4 (.J(out_6), .clk(out_6), .K(out_6), .Q(out_5), .preset(in_3), .reset(in_2));  // open: Qn, en
  J_K_Flip_Flop j_k_ff_5 (.J(out_5), .clk(out_5), .K(out_5), .Q(out_4), .preset(in_3), .reset(in_2));  // open: Qn, en

  // Notes on the sheet:
  //   Filipe Viana de Miranda -- 446415
endmodule
