// Logisim project Exercicio02.circ as structural Verilog: 1 circuit, main circuit main
module main (
  input  in_1,
  input  in_2,
  input  in_3,
  output out_4,
  output out_5,
  output out_6,
  output out_7,
  output out_8
);

  wire clock_1_out, j_k_ff_1_qn, j_k_ff_2_qn, j_k_ff_3_qn, j_k_ff_4_qn;

  Clock clock_1 (.out(clock_1_out));
  J_K_Flip_Flop j_k_ff_1 (
    .J(in_1), .clk(clock_1_out), .K(in_1), .Q(out_8), .Qn(j_k_ff_1_qn), .preset(in_3), .reset(in_2));  // open: en
  J_K_Flip_Flop j_k_ff_2 (
    .J(j_k_ff_1_qn), .clk(j_k_ff_1_qn), .K(j_k_ff_1_qn), .Q(out_7), .Qn(j_k_ff_2_qn), .preset(in_3),
    .reset(in_2));  // open: en
  J_K_Flip_Flop j_k_ff_3 (
    .J(j_k_ff_2_qn), .clk(j_k_ff_2_qn), .K(j_k_ff_2_qn), .Q(out_6), .Qn(j_k_ff_3_qn), .preset(in_3),
    .reset(in_2));  // open: en
  J_K_Flip_Flop j_k_ff_4 (
    .J(j_k_ff_3_qn), .clk(j_k_ff_3_qn), .K(j_k_ff_3_qn), .Q(out_5), .Qn(j_k_ff_4_qn), .preset(in_3),
    .reset(in_2));  // open: en
  J_K_Flip_Flop j_k_ff_5 (
    .J(j_k_ff_4_qn), .clk(j_k_ff_4_qn), .K(j_k_ff_4_qn), .Q(out_4), .preset(in_3), .reset(in_2));  // open: Qn, en

  // Notes on the sheet:
  //   Filipe Viana de Miranda -- 446415
endmodule
