// Logisim project Exercicio03.circ as structural Verilog: 1 circuit, main circuit main
module main (
  input  in_1,
  input  in_2,
  output out_3,
  output out_4,
  output out_5,
  output out_6,
  output out_7
);

  wire and_1_out, clock_1_out, j_k_ff_1_qn, j_k_ff_2_qn, j_k_ff_3_qn, j_k_ff_4_qn, j_k_ff_5_qn, not_1_out,
       not_2_out, not_3_out, not_4_out, or_1_out;

  Clock clock_1 (.out(clock_1_out));
  not not_1 (not_1_out, in_1);
  J_K_Flip_Flop j_k_ff_1 (
    .J(in_1), .clk(clock_1_out), .K(in_1), .Q(out_7), .Qn(j_k_ff_1_qn), .preset(or_1_out), .reset(in_2));  // open: en
  or or_1 (or_1_out, not_1_out, and_1_out);
  not not_2 (not_2_out, j_k_ff_1_qn);
  and and_1 (and_1_out, not_2_out, j_k_ff_2_qn, not_3_out, j_k_ff_4_qn, not_4_out);
  not not_3 (not_3_out, j_k_ff_3_qn);
  not not_4 (not_4_out, j_k_ff_5_qn);
  J_K_Flip_Flop j_k_ff_2 (
    .J(in_1), .clk(out_7), .K(in_1), .Q(out_6), .Qn(j_k_ff_2_qn), .preset(or_1_out), .reset(in_2));  // open: en
  J_K_Flip_Flop j_k_ff_3 (
    .J(in_1), .clk(out_6), .K(in_1), .Q(out_5), .Qn(j_k_ff_3_qn), .preset(or_1_out), .reset(in_2));  // open: en
  J_K_Flip_Flop j_k_ff_4 (
    .J(in_1), .clk(out_5), .K(in_1), .Q(out_4), .Qn(j_k_ff_4_qn), .preset(or_1_out), .reset(in_2));  // open: en
  J_K_Flip_Flop j_k_ff_5 (
    .J(in_1), .clk(out_4), .K(in_1), .Q(out_3), .Qn(j_k_ff_5_qn), .preset(or_1_out), .reset(in_2));  // open: en

  // Notes on the sheet:
  //   Filipe Viana de Miranda -- 446415
endmodule
