// Logisim project Exercicio05.circ as structural Verilog: 1 circuit, main circuit main
module main (
  input  in_1,
  input  in_2,
  output out_3,
  output out_4,
  output out_5,
  output out_6,
  output out_7
);

  wire and_1_out, or_1_out, t_ff_1_qn, t_ff_2_qn, t_ff_3_qn, t_ff_4_qn, t_ff_5_qn;

  or or_1 (or_1_out, in_2, and_1_out);
  T_Flip_Flop t_ff_1 (.clk(t_ff_2_qn), .T(t_ff_2_qn), .Q(out_3), .Qn(t_ff_1_qn), .reset(or_1_out));  // open: preset, en
  and and_1 (and_1_out, t_ff_1_qn, out_4, t_ff_3_qn, t_ff_4_qn, t_ff_5_qn);
  T_Flip_Flop t_ff_2 (.clk(t_ff_3_qn), .T(t_ff_3_qn), .Q(out_4), .Qn(t_ff_2_qn), .reset(or_1_out));  // open: preset, en
  T_Flip_Flop t_ff_3 (.clk(t_ff_4_qn), .T(t_ff_4_qn), .Q(out_5), .Qn(t_ff_3_qn), .reset(or_1_out));  // open: preset, en
  T_Flip_Flop t_ff_4 (.clk(t_ff_5_qn), .T(t_ff_5_qn), .Q(out_6), .Qn(t_ff_4_qn), .reset(or_1_out));  // open: preset, en
  T_Flip_Flop t_ff_5 (.clk(in_1), .T(in_1), .Q(out_7), .Qn(t_ff_5_qn), .reset(or_1_out));  // open: preset, en

  // Notes on the sheet:
  //   Filipe Viana de Miranda -- 446415
endmodule
