// Logisim project guia0901.circ as structural Verilog: 1 circuit, main circuit main
module main (
  input  jk,
  input  pulse,
  input  clr,
  output a,
  output b,
  output c,
  output d,
  output e
);

  J_K_Flip_Flop j_k_ff_1 (.J(jk), .clk(b), .K(jk), .Qn(a), .reset(clr));  // open: Q, preset, en
  J_K_Flip_Flop j_k_ff_2 (.J(jk), .clk(c), .K(jk), .Qn(b), .reset(clr));  // open: Q, preset, en
  J_K_Flip_Flop j_k_ff_3 (.J(jk), .clk(d), .K(jk), .Qn(c), .reset(clr));  // open: Q, preset, en
  J_K_Flip_Flop j_k_ff_4 (.J(jk), .clk(e), .K(jk), .Qn(d), .reset(clr));  // open: Q, preset, en
  J_K_Flip_Flop j_k_ff_5 (.J(jk), .clk(pulse), .K(jk), .Qn(e), .reset(clr));  // open: Q, preset, en
endmodule
