// Logisim project guia0902.circ as structural Verilog: 1 circuit, main circuit main
module main (
  input  jk,
  input  pulse,
  input  clr,
  output a,
  output b,
  output c,
  output d,
  output e
);

  wire j_k_ff_2_q, j_k_ff_3_q, j_k_ff_4_q, j_k_ff_5_q;

  J_K_Flip_Flop j_k_ff_1 (.J(jk), .clk(j_k_ff_2_q), .K(jk), .Qn(a), .reset(clr));  // open: Q, preset, en
  J_K_Flip_Flop j_k_ff_2 (.J(jk), .clk(j_k_ff_3_q), .K(jk), .Q(j_k_ff_2_q), .Qn(b), .reset(clr));  // open: preset, en
  J_K_Flip_Flop j_k_ff_3 (.J(jk), .clk(j_k_ff_4_q), .K(jk), .Q(j_k_ff_3_q), .Qn(c), .reset(clr));  // open: preset, en
  J_K_Flip_Flop j_k_ff_4 (.J(jk), .clk(j_k_ff_5_q), .K(jk), .Q(j_k_ff_4_q), .Qn(d), .reset(clr));  // open: preset, en
  J_K_Flip_Flop j_k_ff_5 (.J(jk), .clk(pulse), .K(jk), .Q(j_k_ff_5_q), .Qn(e), .reset(clr));  // open: preset, en
endmodule
