// Logisim project guia0903.circ as structural Verilog: 1 circuit, main circuit main
module main (
  input  pulse,
  input  jk,
  output a,
  output b,
  output c,
  output d,
  output e
);

  wire and_1_out, j_k_ff_1_qn, j_k_ff_2_qn, j_k_ff_3_qn, j_k_ff_4_qn, j_k_ff_5_qn, not_1_out, not_2_out,
       not_3_out, not_4_out, or_1_out;

  J_K_Flip_Flop j_k_ff_1 (.J(jk), .clk(pulse), .K(jk), .Q(e), .Qn(j_k_ff_1_qn), .preset(or_1_out));  // open: en, reset
  not not_1 (not_1_out, jk);
  and and_1 (and_1_out, not_2_out, j_k_ff_2_qn, not_3_out, j_k_ff_4_qn, not_4_out);
  J_K_Flip_Flop j_k_ff_2 (.J(jk), .clk(e), .K(jk), .Q(d), .Qn(j_k_ff_2_qn), .preset(or_1_out));  // open: en, reset
  or or_1 (or_1_out, not_1_out, and_1_out);
  not not_2 (not_2_out, j_k_ff_1_qn);
  not not_3 (not_3_out, j_k_ff_3_qn);
  J_K_Flip_Flop j_k_ff_3 (.J(jk), .clk(d), .K(jk), .Q(c), .Qn(j_k_ff_3_qn), .preset(or_1_out));  // open: en, reset
  J_K_Flip_Flop j_k_ff_4 (.J(jk), .clk(c), .K(jk), .Q(b), .Qn(j_k_ff_4_qn), .preset(or_1_out));  // open: en, reset
  not not_4 (not_4_out, j_k_ff_5_qn);
  J_K_Flip_Flop j_k_ff_5 (.J(jk), .clk(b), .K(jk), .Q(a), .Qn(j_k_ff_5_qn), .preset(or_1_out));  // open: en, reset
endmodule
