// Logisim project guia0904.circ as structural Verilog: 1 circuit, main circuit main
module main (
  input  jk,
  input  pulse,
  input  clr,
  output a,
  output b,
  output c,
  output d,
  output e
);

  wire and_1_out, and_2_out, j_k_ff_1_qn, j_k_ff_2_qn, j_k_ff_3_qn, j_k_ff_4_qn, not_1_out, not_2_out;

  J_K_Flip_Flop j_k_ff_1 (.J(jk), .clk(pulse), .K(jk), .Q(e), .Qn(j_k_ff_1_qn), .reset(and_1_out));  // open: preset, en
  and and_1 (and_1_out, clr, and_2_out);
  and and_2 (and_2_out, e, not_1_out, c, not_2_out, a);
  J_K_Flip_Flop j_k_ff_2 (
    .J(jk), .clk(j_k_ff_1_qn), .K(jk), .Q(d), .Qn(j_k_ff_2_qn), .reset(and_1_out));  // open: preset, en
  not not_1 (not_1_out, d);
  J_K_Flip_Flop j_k_ff_3 (
    .J(jk), .clk(j_k_ff_2_qn), .K(jk), .Q(c), .Qn(j_k_ff_3_qn), .reset(and_1_out));  // open: preset, en
  J_K_Flip_Flop j_k_ff_4 (
    .J(jk), .clk(j_k_ff_3_qn), .K(jk), .Q(b), .Qn(j_k_ff_4_qn), .reset(and_1_out));  // open: preset, en
  not not_2 (not_2_out, b);
  J_K_Flip_Flop j_k_ff_5 (.J(jk), .clk(j_k_ff_4_qn), .K(jk), .Q(a), .reset(and_1_out));  // open: Qn, preset, en
endmodule
