// Logisim project guia0905.circ as structural Verilog: 1 circuit, main circuit main
module main (
  input  pulse,
  input  clr,
  output d,
  output c,
  output b,
  output a
);

  wire and_1_out, not_1_out, not_2_out, not_3_out, or_1_out, t_ff_2_qn, t_ff_3_qn, t_ff_4_qn;

  and and_1 (and_1_out, d, not_2_out, not_3_out, not_1_out);
  T_Flip_Flop t_ff_1 (.clk(t_ff_2_qn), .T(t_ff_2_qn), .Q(d), .reset(or_1_out));  // open: Qn, preset, en
  or or_1 (or_1_out, clr, and_1_out);
  not not_1 (not_1_out, a);
  not not_2 (not_2_out, c);
  T_Flip_Flop t_ff_2 (.clk(t_ff_3_qn), .T(t_ff_3_qn), .Q(c), .Qn(t_ff_2_qn), .reset(or_1_out));  // open: preset, en
  not not_3 (not_3_out, b);
  T_Flip_Flop t_ff_3 (.clk(t_ff_4_qn), .T(t_ff_4_qn), .Q(b), .Qn(t_ff_3_qn), .reset(or_1_out));  // open: preset, en
  T_Flip_Flop t_ff_4 (.clk(pulse), .T(pulse), .Q(a), .Qn(t_ff_4_qn), .reset(or_1_out));  // open: preset, en
endmodule
