// Logisim project Exercicio0001.circ as structural Verilog: 1 circuit, main circuit main
module main (
  input  PULSE,
  input  CLR,
  input  _1,
  output a,
  output b,
  output c,
  output d,
  output e
);

  J_K_Flip_Flop j_k_ff_1 (.J(_1), .clk(b), .K(_1), .Qn(a), .reset(CLR));  // open: Q, preset, en
  J_K_Flip_Flop j_k_ff_2 (.J(_1), .clk(c), .K(_1), .Qn(b), .reset(CLR));  // open: Q, preset, en
  J_K_Flip_Flop j_k_ff_3 (.J(_1), .clk(d), .K(_1), .Qn(c), .reset(CLR));  // open: Q, preset, en
  J_K_Flip_Flop j_k_ff_4 (.J(_1), .clk(e), .K(_1), .Qn(d), .reset(CLR));  // open: Q, preset, en
  J_K_Flip_Flop j_k_ff_5 (.J(_1), .clk(PULSE), .K(_1), .Qn(e), .reset(CLR));  // open: Q, preset, en

  // Notes on the sheet:
  //   João Henrique - 392734
endmodule
