// Logisim project Exercicio0002.circ as structural Verilog: 1 circuit, main circuit main
module main (
  input  PULSE,
  input  CLR,
  input  _1,
  output a,
  output b,
  output c,
  output d,
  output e
);

  wire j_k_ff_2_q, j_k_ff_3_q, j_k_ff_4_q, j_k_ff_5_q;

  J_K_Flip_Flop j_k_ff_1 (.J(_1), .clk(j_k_ff_2_q), .K(_1), .Qn(a), .reset(CLR));  // open: Q, preset, en
  J_K_Flip_Flop j_k_ff_2 (.J(_1), .clk(j_k_ff_3_q), .K(_1), .Q(j_k_ff_2_q), .Qn(b), .reset(CLR));  // open: preset, en
  J_K_Flip_Flop j_k_ff_3 (.J(_1), .clk(j_k_ff_4_q), .K(_1), .Q(j_k_ff_3_q), .Qn(c), .reset(CLR));  // open: preset, en
  J_K_Flip_Flop j_k_ff_4 (.J(_1), .clk(j_k_ff_5_q), .K(_1), .Q(j_k_ff_4_q), .Qn(d), .reset(CLR));  // open: preset, en
  J_K_Flip_Flop j_k_ff_5 (.J(_1), .clk(PULSE), .K(_1), .Q(j_k_ff_5_q), .Qn(e), .reset(CLR));  // open: preset, en

  // Notes on the sheet:
  //   João Henrique - 392734
endmodule
