// Logisim project Exercicio0003.circ as structural Verilog: 1 circuit, main circuit main
module main (
  input  _1,
  input  pulse,
  input  clear,
  output out_4,
  output out_5,
  output out_6,
  output out_7,
  output out_8
);

  wire and_1_out, j_k_ff_2_qn, j_k_ff_4_qn, not_1_out, or_1_out;

  not not_1 (not_1_out, _1);
  or or_1 (or_1_out, not_1_out, and_1_out);
  and and_1 (and_1_out, out_8, j_k_ff_2_qn, out_6, j_k_ff_4_qn, out_4);
  J_K_Flip_Flop j_k_ff_1 (.J(_1), .clk(pulse), .K(_1), .Q(out_8), .preset(or_1_out), .reset(clear));  // open: Qn, en
  J_K_Flip_Flop j_k_ff_2 (
    .J(_1), .clk(out_8), .K(_1), .Q(out_7), .Qn(j_k_ff_2_qn), .preset(or_1_out), .reset(clear));  // open: en
  J_K_Flip_Flop j_k_ff_3 (.J(_1), .clk(out_7), .K(_1), .Q(out_6), .preset(or_1_out), .reset(clear));  // open: Qn, en
  J_K_Flip_Flop j_k_ff_4 (
    .J(_1), .clk(out_6), .K(_1), .Q(out_5), .Qn(j_k_ff_4_qn), .preset(or_1_out), .reset(clear));  // open: en
  // Probe on {out_4, out_5, out_6, out_7, out_8}
  J_K_Flip_Flop j_k_ff_5 (.J(_1), .clk(out_5), .K(_1), .Q(out_4), .preset(or_1_out), .reset(clear));  // open: Qn, en

  // Notes on the sheet:
  //   João Henrique - 392734
endmodule
