// Logisim project Exercicio0004.circ as structural Verilog: 1 circuit, main circuit main
module main (
  input  _1,
  input  PULSE,
  input  CLR,
  output a,
  output b,
  output c,
  output d,
  output e
);

  wire j_k_ff_1_qn, j_k_ff_2_qn, j_k_ff_3_qn, j_k_ff_4_qn, j_k_ff_5_qn, nand_1_out, nand_2_out;

  nand nand_1 (nand_1_out, CLR, nand_2_out);
  nand nand_2 (nand_2_out, j_k_ff_1_qn, d, j_k_ff_3_qn, b, j_k_ff_5_qn);
  J_K_Flip_Flop j_k_ff_1 (
    .J(_1), .clk(PULSE), .K(_1), .Q(e), .Qn(j_k_ff_1_qn), .reset(nand_1_out));  // open: preset, en
  J_K_Flip_Flop j_k_ff_2 (
    .J(_1), .clk(j_k_ff_1_qn), .K(_1), .Q(d), .Qn(j_k_ff_2_qn), .reset(nand_1_out));  // open: preset, en
  J_K_Flip_Flop j_k_ff_3 (
    .J(_1), .clk(j_k_ff_2_qn), .K(_1), .Q(c), .Qn(j_k_ff_3_qn), .reset(nand_1_out));  // open: preset, en
  // Probe on {a, b, c, d, e}
  J_K_Flip_Flop j_k_ff_4 (
    .J(_1), .clk(j_k_ff_3_qn), .K(_1), .Q(b), .Qn(j_k_ff_4_qn), .reset(nand_1_out));  // open: preset, en
  J_K_Flip_Flop j_k_ff_5 (
    .J(_1), .clk(j_k_ff_4_qn), .K(_1), .Q(a), .Qn(j_k_ff_5_qn), .reset(nand_1_out));  // open: preset, en

  // Notes on the sheet:
  //   João Henrique - 392734
endmodule
