// Logisim project Exercicio0007.circ as structural Verilog: 1 circuit, main circuit main
module main (
  input  INPUT,
  input  CLR,
  output a,
  output b,
  output c,
  output d,
  output e
);

  wire CLK_out, j_k_ff_1_qn, j_k_ff_2_qn, j_k_ff_3_qn, j_k_ff_4_qn, j_k_ff_5_qn, not_1_out, or_1_out;

  Clock CLK (.out(CLK_out));
  or or_1 (or_1_out, j_k_ff_5_qn, INPUT);
  not not_1 (not_1_out, or_1_out);
  J_K_Flip_Flop j_k_ff_1 (
    .J(or_1_out), .clk(CLK_out), .K(not_1_out), .Q(a), .Qn(j_k_ff_1_qn), .reset(CLR));  // open: preset, en
  J_K_Flip_Flop j_k_ff_2 (
    .J(a), .clk(CLK_out), .K(j_k_ff_1_qn), .Q(b), .Qn(j_k_ff_2_qn), .reset(CLR));  // open: preset, en
  J_K_Flip_Flop j_k_ff_3 (
    .J(b), .clk(CLK_out), .K(j_k_ff_2_qn), .Q(c), .Qn(j_k_ff_3_qn), .reset(CLR));  // open: preset, en
  J_K_Flip_Flop j_k_ff_4 (
    .J(c), .clk(CLK_out), .K(j_k_ff_3_qn), .Q(d), .Qn(j_k_ff_4_qn), .reset(CLR));  // open: preset, en
  J_K_Flip_Flop j_k_ff_5 (
    .J(d), .clk(CLK_out), .K(j_k_ff_4_qn), .Q(e), .Qn(j_k_ff_5_qn), .reset(CLR));  // open: preset, en
  // Probe on {a, b, c, d, e}

  // Notes on the sheet:
  //   João Henrique - 392734
endmodule
