// Logisim project Exercicio005.circ as structural Verilog: 1 circuit, main circuit main
module main (
  input  pulso,
  input  CLR,
  output h,
  output g,
  output f,
  output e
);

  wire and_1_out, not_1_out, not_2_out, or_1_out, t_ff_2_qn, t_ff_3_qn, t_ff_4_qn;

  T_Flip_Flop t_ff_1 (.clk(t_ff_2_qn), .T(t_ff_2_qn), .Q(h), .reset(or_1_out));  // open: Qn, preset, en
  or or_1 (or_1_out, CLR, and_1_out);
  T_Flip_Flop t_ff_2 (.clk(t_ff_3_qn), .T(t_ff_3_qn), .Q(g), .Qn(t_ff_2_qn), .reset(or_1_out));  // open: preset, en
  not not_1 (not_1_out, g);
  not not_2 (not_2_out, f);
  and and_1 (and_1_out, h, not_1_out, not_2_out, e);
  T_Flip_Flop t_ff_3 (.clk(t_ff_4_qn), .T(t_ff_4_qn), .Q(f), .Qn(t_ff_3_qn), .reset(or_1_out));  // open: preset, en
  T_Flip_Flop t_ff_4 (.clk(pulso), .T(pulso), .Q(e), .Qn(t_ff_4_qn), .reset(or_1_out));  // open: preset, en

  // Notes on the sheet:
  //   Fernando Silva
endmodule
