// Logisim project Extra01.circ as structural Verilog: 1 circuit, main circuit main
module main (
  input  clock,
  input  \input ,
  input  clear,
  output a,
  output b,
  output c,
  output d,
  output e
);

  wire not_1_out, not_2_out, not_3_out, not_4_out, not_5_out, or_1_out;

  or or_1 (or_1_out, e, \input );
  not not_1 (not_1_out, or_1_out);
  J_K_Flip_Flop j_k_ff_1 (.J(or_1_out), .clk(clock), .K(not_1_out), .Q(a), .reset(clear));  // open: Qn, preset, en
  not not_2 (not_2_out, a);
  J_K_Flip_Flop j_k_ff_2 (.J(a), .clk(clock), .K(not_2_out), .Q(b), .reset(clear));  // open: Qn, preset, en
  J_K_Flip_Flop j_k_ff_3 (.J(b), .clk(clock), .K(not_3_out), .Q(c), .reset(clear));  // open: Qn, preset, en
  not not_3 (not_3_out, b);
  J_K_Flip_Flop j_k_ff_4 (.J(c), .clk(clock), .K(not_4_out), .Q(d), .reset(clear));  // open: Qn, preset, en
  not not_4 (not_4_out, c);
  J_K_Flip_Flop j_k_ff_5 (.J(d), .clk(clock), .K(not_5_out), .Q(e), .reset(clear));  // open: Qn, preset, en
  not not_5 (not_5_out, d);
endmodule
