// Logisim project Circuitos.circ as structural Verilog
module Exercicio1 (
  input  dt,
  input  clr,
  output out_3,
  output out_4,
  output out_5,
  output out_6,
  output out_7
);

  wire clk_out;

  Clock clk (.out(clk_out));
  J_K_Flip_Flop j_k_ff_1 (.J(dt), .clk(out_4), .K(dt), .Qn(out_3), .reset(clr));  // open: Q, preset, en
  J_K_Flip_Flop j_k_ff_2 (.J(dt), .clk(out_5), .K(dt), .Qn(out_4), .reset(clr));  // open: Q, preset, en
  J_K_Flip_Flop j_k_ff_3 (.J(dt), .clk(out_6), .K(dt), .Qn(out_5), .reset(clr));  // open: Q, preset, en
  J_K_Flip_Flop j_k_ff_4 (.J(dt), .clk(out_7), .K(dt), .Qn(out_6), .reset(clr));  // open: Q, preset, en
  J_K_Flip_Flop j_k_ff_5 (.J(dt), .clk(clk_out), .K(dt), .Qn(out_7), .reset(clr));  // open: Q, preset, en
endmodule

module Exercicio2 (
  input  dt,
  input  clr,
  output out_3,
  output out_4,
  output out_5,
  output out_6,
  output out_7
);

  wire clk_out, j_k_ff_2_q, j_k_ff_3_q, j_k_ff_4_q, j_k_ff_5_q;

  Clock clk (.out(clk_out));
  J_K_Flip_Flop j_k_ff_1 (.J(dt), .clk(j_k_ff_2_q), .K(dt), .Qn(out_3), .reset(clr));  // open: Q, preset, en
  J_K_Flip_Flop j_k_ff_2 (
    .J(dt), .clk(j_k_ff_3_q), .K(dt), .Q(j_k_ff_2_q), .Qn(out_4), .reset(clr));  // open: preset, en
  J_K_Flip_Flop j_k_ff_3 (
    .J(dt), .clk(j_k_ff_4_q), .K(dt), .Q(j_k_ff_3_q), .Qn(out_5), .reset(clr));  // open: preset, en
  J_K_Flip_Flop j_k_ff_4 (
    .J(dt), .clk(j_k_ff_5_q), .K(dt), .Q(j_k_ff_4_q), .Qn(out_6), .reset(clr));  // open: preset, en
  J_K_Flip_Flop j_k_ff_5 (.J(dt), .clk(clk_out), .K(dt), .Q(j_k_ff_5_q), .Qn(out_7), .reset(clr));  // open: preset, en
endmodule

module Exercicio3 (
  input  dt,
  output out_2,
  output out_3,
  output out_4,
  output out_5,
  output out_6
);

  wire and_1_out, clk_out, j_k_ff_2_qn, j_k_ff_4_qn, not_1_out, or_1_out;

  Clock clk (.out(clk_out));
  not not_1 (not_1_out, dt);
  J_K_Flip_Flop j_k_ff_1 (.J(dt), .clk(clk_out), .K(dt), .Q(out_6), .preset(or_1_out));  // open: Qn, en, reset
  or or_1 (or_1_out, not_1_out, and_1_out);
  and and_1 (and_1_out, out_6, j_k_ff_2_qn, out_4, j_k_ff_4_qn, out_2);
  J_K_Flip_Flop j_k_ff_2 (
    .J(dt), .clk(out_6), .K(dt), .Q(out_5), .Qn(j_k_ff_2_qn), .preset(or_1_out));  // open: en, reset
  J_K_Flip_Flop j_k_ff_3 (.J(dt), .clk(out_5), .K(dt), .Q(out_4), .preset(or_1_out));  // open: Qn, en, reset
  J_K_Flip_Flop j_k_ff_4 (
    .J(dt), .clk(out_4), .K(dt), .Q(out_3), .Qn(j_k_ff_4_qn), .preset(or_1_out));  // open: en, reset
  J_K_Flip_Flop j_k_ff_5 (.J(dt), .clk(out_3), .K(dt), .Q(out_2), .preset(or_1_out));  // open: Qn, en, reset
endmodule

module Exercicio4 (
  input  dt,
  input  clr,
  output out_3,
  output out_4,
  output out_5,
  output out_6,
  output out_7
);

  wire clk_out, j_k_ff_1_qn, j_k_ff_2_qn, j_k_ff_3_qn, j_k_ff_4_qn, j_k_ff_5_qn, nand_1_out, nand_2_out;

  Clock clk (.out(clk_out));
  nand nand_1 (nand_1_out, j_k_ff_1_qn, out_6, j_k_ff_3_qn, out_4, j_k_ff_5_qn);
  J_K_Flip_Flop j_k_ff_1 (
    .J(dt), .clk(clk_out), .K(dt), .Q(out_7), .Qn(j_k_ff_1_qn), .reset(nand_2_out));  // open: preset, en
  nand nand_2 (nand_2_out, clr, nand_1_out);
  J_K_Flip_Flop j_k_ff_2 (
    .J(dt), .clk(j_k_ff_1_qn), .K(dt), .Q(out_6), .Qn(j_k_ff_2_qn), .reset(nand_2_out));  // open: preset, en
  J_K_Flip_Flop j_k_ff_3 (
    .J(dt), .clk(j_k_ff_2_qn), .K(dt), .Q(out_5), .Qn(j_k_ff_3_qn), .reset(nand_2_out));  // open: preset, en
  J_K_Flip_Flop j_k_ff_4 (
    .J(dt), .clk(j_k_ff_3_qn), .K(dt), .Q(out_4), .Qn(j_k_ff_4_qn), .reset(nand_2_out));  // open: preset, en
  J_K_Flip_Flop j_k_ff_5 (
    .J(dt), .clk(j_k_ff_4_qn), .K(dt), .Q(out_3), .Qn(j_k_ff_5_qn), .reset(nand_2_out));  // open: preset, en
endmodule

module Exercicio5 (
  input  dt,
  input  clr,
  output out_3,
  output out_4,
  output out_5,
  output out_6
);

  wire and_1_out, or_1_out, t_ff_2_qn, t_ff_3_qn, t_ff_4_qn;

  and and_1 (and_1_out, out_3, t_ff_2_qn, t_ff_3_qn, t_ff_4_qn);
  T_Flip_Flop t_ff_1 (.clk(t_ff_2_qn), .T(t_ff_2_qn), .Q(out_3), .reset(or_1_out));  // open: Qn, preset, en
  or or_1 (or_1_out, clr, and_1_out);
  T_Flip_Flop t_ff_2 (.clk(t_ff_3_qn), .T(t_ff_3_qn), .Q(out_4), .Qn(t_ff_2_qn), .reset(or_1_out));  // open: preset, en
  T_Flip_Flop t_ff_3 (.clk(t_ff_4_qn), .T(t_ff_4_qn), .Q(out_5), .Qn(t_ff_3_qn), .reset(or_1_out));  // open: preset, en
  T_Flip_Flop t_ff_4 (.clk(dt), .T(dt), .Q(out_6), .Qn(t_ff_4_qn), .reset(or_1_out));  // open: preset, en
endmodule

module Exercicio6 (
  input  dt,
  input  clr,
  output out_3,
  output out_4,
  output out_5,
  output out_6,
  output out_7
);

  wire clk_out, not_1_out, not_2_out, not_3_out, not_4_out, not_5_out, or_1_out;

  Clock clk (.out(clk_out));
  not not_1 (not_1_out, or_1_out);
  or or_1 (or_1_out, dt, out_7);
  J_K_Flip_Flop j_k_ff_1 (.J(or_1_out), .clk(clk_out), .K(not_1_out), .Q(out_3), .reset(clr));  // open: Qn, preset, en
  not not_2 (not_2_out, out_3);
  J_K_Flip_Flop j_k_ff_2 (.J(out_3), .clk(clk_out), .K(not_2_out), .Q(out_4), .reset(clr));  // open: Qn, preset, en
  J_K_Flip_Flop j_k_ff_3 (.J(out_4), .clk(clk_out), .K(not_3_out), .Q(out_5), .reset(clr));  // open: Qn, preset, en
  not not_3 (not_3_out, out_4);
  J_K_Flip_Flop j_k_ff_4 (.J(out_5), .clk(clk_out), .K(not_4_out), .Q(out_6), .reset(clr));  // open: Qn, preset, en
  not not_4 (not_4_out, out_5);
  J_K_Flip_Flop j_k_ff_5 (.J(out_6), .clk(clk_out), .K(not_5_out), .Q(out_7), .reset(clr));  // open: Qn, preset, en
  not not_5 (not_5_out, out_6);
endmodule

module Exercicio7 (
  input  clr,
  output out_2,
  output out_3,
  output out_4,
  output out_5,
  output out_6
);

  wire clk_out, j_k_ff_5_qn, not_1_out, not_2_out, not_3_out, not_4_out, not_5_out;

  Clock clk (.out(clk_out));
  J_K_Flip_Flop j_k_ff_1 (
    .J(j_k_ff_5_qn), .clk(clk_out), .K(not_1_out), .Q(out_2), .reset(clr));  // open: Qn, preset, en
  not not_1 (not_1_out, j_k_ff_5_qn);
  J_K_Flip_Flop j_k_ff_2 (.J(out_2), .clk(clk_out), .K(not_2_out), .Q(out_3), .reset(clr));  // open: Qn, preset, en
  not not_2 (not_2_out, out_2);
  J_K_Flip_Flop j_k_ff_3 (.J(out_3), .clk(clk_out), .K(not_3_out), .Q(out_4), .reset(clr));  // open: Qn, preset, en
  not not_3 (not_3_out, out_3);
  J_K_Flip_Flop j_k_ff_4 (.J(out_4), .clk(clk_out), .K(not_4_out), .Q(out_5), .reset(clr));  // open: Qn, preset, en
  not not_4 (not_4_out, out_4);
  not not_5 (not_5_out, out_5);
  J_K_Flip_Flop j_k_ff_5 (
    .J(out_5), .clk(clk_out), .K(not_5_out), .Q(out_6), .Qn(j_k_ff_5_qn), .reset(clr));  // open: preset, en
endmodule
