// Logisim project Exercicio01.circ as structural Verilog: 1 circuit, main circuit main
module main (
  input  PULSE,
  input  In,
  input  CLR,
  output a,
  output b,
  output c,
  output d,
  output e
);

  J_K_Flip_Flop u_A (.J(In), .clk(b), .K(In), .Qn(a), .reset(CLR));  // open: Q, preset, en
  J_K_Flip_Flop u_B (.J(In), .clk(c), .K(In), .Qn(b), .reset(CLR));  // open: Q, preset, en
  J_K_Flip_Flop u_C (.J(In), .clk(d), .K(In), .Qn(c), .reset(CLR));  // open: Q, preset, en
  J_K_Flip_Flop u_D (.J(In), .clk(e), .K(In), .Qn(d), .reset(CLR));  // open: Q, preset, en
  J_K_Flip_Flop u_E (.J(In), .clk(PULSE), .K(In), .Qn(e), .reset(CLR));  // open: Q, preset, en
endmodule
