// Logisim project Exercicio02.circ as structural Verilog: 1 circuit, main circuit main
module main (
  input  PULSE,
  input  In,
  input  CLR,
  input  PRESET,
  output a,
  output b,
  output c,
  output d,
  output e
);

  wire B_q, C_q, D_q, E_q;

  J_K_Flip_Flop u_A (.J(In), .clk(B_q), .K(In), .Qn(a), .preset(PRESET), .reset(CLR));  // open: Q, en
  J_K_Flip_Flop u_B (.J(In), .clk(C_q), .K(In), .Q(B_q), .Qn(b), .preset(PRESET), .reset(CLR));  // open: en
  J_K_Flip_Flop u_C (.J(In), .clk(D_q), .K(In), .Q(C_q), .Qn(c), .preset(PRESET), .reset(CLR));  // open: en
  J_K_Flip_Flop u_D (.J(In), .clk(E_q), .K(In), .Q(D_q), .Qn(d), .preset(PRESET), .reset(CLR));  // open: en
  J_K_Flip_Flop u_E (.J(In), .clk(PULSE), .K(In), .Q(E_q), .Qn(e), .preset(PRESET), .reset(CLR));  // open: en
endmodule
