// Logisim project Exercicio03.circ as structural Verilog: 1 circuit, main circuit main
module main (
  input  IN,
  input  PULSE,
  input  CLR,
  output out_4,
  output out_5,
  output out_6,
  output out_7,
  output out_8
);

  wire A_qn, and_1_out, B_qn, C_qn, D_qn, E_qn, not_1_out, not_2_out, not_3_out, not_4_out, or_1_out;

  not not_1 (not_1_out, IN);
  and and_1 (and_1_out, not_2_out, D_qn, not_3_out, B_qn, not_4_out);
  J_K_Flip_Flop E (.J(IN), .clk(PULSE), .K(IN), .Q(out_8), .Qn(E_qn), .preset(or_1_out), .reset(CLR));  // open: en
  or or_1 (or_1_out, not_1_out, and_1_out);
  not not_2 (not_2_out, E_qn);
  not not_3 (not_3_out, C_qn);
  not not_4 (not_4_out, A_qn);
  J_K_Flip_Flop D (.J(IN), .clk(out_8), .K(IN), .Q(out_7), .Qn(D_qn), .preset(or_1_out), .reset(CLR));  // open: en
  J_K_Flip_Flop C (.J(IN), .clk(out_7), .K(IN), .Q(out_6), .Qn(C_qn), .preset(or_1_out), .reset(CLR));  // open: en
  J_K_Flip_Flop B (.J(IN), .clk(out_6), .K(IN), .Q(out_5), .Qn(B_qn), .preset(or_1_out), .reset(CLR));  // open: en
  J_K_Flip_Flop A (.J(IN), .clk(out_5), .K(IN), .Q(out_4), .Qn(A_qn), .preset(or_1_out), .reset(CLR));  // open: en
endmodule
