// Logisim project Exercicio04.circ as structural Verilog: 1 circuit, main circuit main
module main (
  input  IN,
  input  PULSE,
  input  CLR,
  output a,
  output b,
  output c,
  output d,
  output e
);

  wire B_qn, C_qn, D_qn, E_qn, nand_1_out, nand_2_out, not_1_out, not_2_out, not_3_out;

  nand nand_1 (nand_1_out, not_1_out, d, not_2_out, b, not_3_out);
  J_K_Flip_Flop u_E (.J(IN), .clk(PULSE), .K(IN), .Q(e), .Qn(E_qn), .reset(nand_2_out));  // open: preset, en
  nand nand_2 (nand_2_out, CLR, nand_1_out);
  not not_1 (not_1_out, e);
  not not_2 (not_2_out, c);
  not not_3 (not_3_out, a);
  J_K_Flip_Flop u_D (.J(IN), .clk(E_qn), .K(IN), .Q(d), .Qn(D_qn), .reset(nand_2_out));  // open: preset, en
  J_K_Flip_Flop u_C (.J(IN), .clk(D_qn), .K(IN), .Q(c), .Qn(C_qn), .reset(nand_2_out));  // open: preset, en
  J_K_Flip_Flop u_B (.J(IN), .clk(C_qn), .K(IN), .Q(b), .Qn(B_qn), .reset(nand_2_out));  // open: preset, en
  J_K_Flip_Flop u_A (.J(IN), .clk(B_qn), .K(IN), .Q(a), .reset(nand_2_out));  // open: Qn, preset, en
endmodule
