// Logisim project Exercicio05.circ as structural Verilog: 1 circuit, main circuit main
module main (
  input  IN,
  input  CLR,
  output a,
  output b,
  output c,
  output d
);

  wire and_1_out, B_qn, C_qn, D_qn, or_1_out;

  and and_1 (and_1_out, a, B_qn, C_qn, D_qn);
  or or_1 (or_1_out, CLR, and_1_out);
  T_Flip_Flop u_A (.clk(B_qn), .T(B_qn), .Q(a), .reset(or_1_out));  // open: Qn, preset, en
  T_Flip_Flop u_B (.clk(C_qn), .T(C_qn), .Q(b), .Qn(B_qn), .reset(or_1_out));  // open: preset, en
  T_Flip_Flop u_C (.clk(D_qn), .T(D_qn), .Q(c), .Qn(C_qn), .reset(or_1_out));  // open: preset, en
  T_Flip_Flop u_D (.clk(IN), .T(IN), .Q(d), .Qn(D_qn), .reset(or_1_out));  // open: preset, en
endmodule
