// Logisim project Exercicio01.circ as structural Verilog: 1 circuit, main circuit main
module main (
  input  _1,
  input  CLR,
  output A,
  output B,
  output C,
  output D,
  output E
);

  wire PULSE_out;

  Clock PULSE (.out(PULSE_out));
  J_K_Flip_Flop j_k_ff_1 (.J(_1), .clk(B), .K(_1), .Qn(A), .reset(CLR));  // open: Q, preset, en
  J_K_Flip_Flop j_k_ff_2 (.J(_1), .clk(C), .K(_1), .Qn(B), .reset(CLR));  // open: Q, preset, en
  J_K_Flip_Flop j_k_ff_3 (.J(_1), .clk(D), .K(_1), .Qn(C), .reset(CLR));  // open: Q, preset, en
  J_K_Flip_Flop j_k_ff_4 (.J(_1), .clk(E), .K(_1), .Qn(D), .reset(CLR));  // open: Q, preset, en
  J_K_Flip_Flop j_k_ff_5 (.J(_1), .clk(PULSE_out), .K(_1), .Qn(E), .reset(CLR));  // open: Q, preset, en
endmodule
