// Logisim project Exercicio03.circ as structural Verilog: 1 circuit, main circuit main
module main (
  input  _1,
  input  CLR,
  output A,
  output B,
  output C,
  output D,
  output E
);

  wire and_1_out, j_k_ff_1_qn, j_k_ff_2_qn, j_k_ff_3_qn, j_k_ff_4_qn, j_k_ff_5_qn, not_1_out, not_2_out,
       not_3_out, not_4_out, or_1_out, PULSE_out;

  Clock PULSE (.out(PULSE_out));
  not not_1 (not_1_out, _1);
  J_K_Flip_Flop j_k_ff_1 (
    .J(_1), .clk(PULSE_out), .K(_1), .Q(E), .Qn(j_k_ff_1_qn), .preset(or_1_out));  // open: en, reset
  or or_1 (or_1_out, not_1_out, and_1_out);
  not not_2 (not_2_out, j_k_ff_1_qn);
  not not_3 (not_3_out, j_k_ff_3_qn);
  and and_1 (and_1_out, not_2_out, j_k_ff_2_qn, not_3_out, j_k_ff_4_qn, not_4_out);
  not not_4 (not_4_out, j_k_ff_5_qn);
  J_K_Flip_Flop j_k_ff_2 (.J(_1), .clk(E), .K(_1), .Q(D), .Qn(j_k_ff_2_qn), .preset(or_1_out));  // open: en, reset
  J_K_Flip_Flop j_k_ff_3 (
    .J(_1), .clk(D), .K(_1), .Q(C), .Qn(j_k_ff_3_qn), .preset(or_1_out), .reset(CLR));  // open: en
  J_K_Flip_Flop j_k_ff_4 (
    .J(_1), .clk(C), .K(_1), .Q(B), .Qn(j_k_ff_4_qn), .preset(or_1_out), .reset(CLR));  // open: en
  J_K_Flip_Flop j_k_ff_5 (
    .J(_1), .clk(B), .K(_1), .Q(A), .Qn(j_k_ff_5_qn), .preset(or_1_out), .reset(CLR));  // open: en
endmodule
