// Logisim project Exercicio01.circ as structural Verilog: 1 circuit, main circuit main
module main (
  input  pulse,
  input  _1,
  input  CLR,
  output q1not,
  output q2not,
  output q3not,
  output out_7,
  output out_8
);

  J_K_Flip_Flop j_k_ff_1 (.J(_1), .clk(q2not), .K(_1), .Qn(q1not), .reset(CLR));  // open: Q, preset, en
  J_K_Flip_Flop j_k_ff_2 (.J(_1), .clk(q3not), .K(_1), .Qn(q2not), .reset(CLR));  // open: Q, preset, en
  J_K_Flip_Flop j_k_ff_3 (.J(_1), .clk(out_7), .K(_1), .Qn(q3not), .reset(CLR));  // open: Q, preset, en
  J_K_Flip_Flop j_k_ff_4 (.J(_1), .clk(out_8), .K(_1), .Qn(out_7), .reset(CLR));  // open: Q, preset, en
  J_K_Flip_Flop j_k_ff_5 (.J(_1), .clk(pulse), .K(_1), .Qn(out_8), .reset(CLR));  // open: Q, preset, en

  // Notes on the sheet:
  //   qnot
  //   q4not
endmodule
