// Logisim project Exercicio02.circ as structural Verilog: 1 circuit, main circuit main
module main (
  input  pulse,
  input  _1,
  input  CLR,
  output q1,
  output q2,
  output q3,
  output out_7,
  output out_8
);

  wire j_k_ff_2_q, j_k_ff_3_q, j_k_ff_4_q, j_k_ff_5_q;

  J_K_Flip_Flop j_k_ff_1 (
    .J(j_k_ff_2_q), .clk(j_k_ff_2_q), .K(j_k_ff_2_q), .Qn(q1), .reset(CLR));  // open: Q, preset, en
  J_K_Flip_Flop j_k_ff_2 (
    .J(j_k_ff_3_q), .clk(j_k_ff_3_q), .K(j_k_ff_3_q), .Q(j_k_ff_2_q), .Qn(q2), .reset(CLR));  // open: preset, en
  J_K_Flip_Flop j_k_ff_3 (
    .J(j_k_ff_4_q), .clk(j_k_ff_4_q), .K(j_k_ff_4_q), .Q(j_k_ff_3_q), .Qn(q3), .reset(CLR));  // open: preset, en
  J_K_Flip_Flop j_k_ff_4 (
    .J(j_k_ff_5_q), .clk(j_k_ff_5_q), .K(j_k_ff_5_q), .Q(j_k_ff_4_q), .Qn(out_7), .reset(CLR));  // open: preset, en
  J_K_Flip_Flop j_k_ff_5 (.J(_1), .clk(pulse), .K(_1), .Q(j_k_ff_5_q), .Qn(out_8), .reset(CLR));  // open: preset, en

  // Notes on the sheet:
  //   q4
endmodule
