// Logisim project Exercicio03.circ as structural Verilog: 1 circuit, main circuit main
module main (
  input  _1,
  input  pulse,
  output q4,
  output q3,
  output q2,
  output q1,
  output q
);

  wire and_1_out, j_k_ff_1_qn, j_k_ff_2_qn, j_k_ff_3_qn, j_k_ff_4_qn, j_k_ff_5_qn, not_1_out, not_2_out,
       not_3_out, not_4_out, or_1_out;

  not not_1 (not_1_out, _1);
  and and_1 (and_1_out, not_2_out, j_k_ff_2_qn, not_3_out, j_k_ff_4_qn, not_4_out);
  J_K_Flip_Flop j_k_ff_1 (.J(_1), .clk(pulse), .K(_1), .Q(q), .Qn(j_k_ff_1_qn), .preset(or_1_out));  // open: en, reset
  or or_1 (or_1_out, not_1_out, and_1_out);
  not not_2 (not_2_out, j_k_ff_1_qn);
  not not_3 (not_3_out, j_k_ff_3_qn);
  not not_4 (not_4_out, j_k_ff_5_qn);
  J_K_Flip_Flop j_k_ff_2 (.J(_1), .clk(q), .K(_1), .Q(q1), .Qn(j_k_ff_2_qn), .preset(or_1_out));  // open: en, reset
  J_K_Flip_Flop j_k_ff_3 (.J(_1), .clk(q1), .K(_1), .Q(q2), .Qn(j_k_ff_3_qn), .preset(or_1_out));  // open: en, reset
  J_K_Flip_Flop j_k_ff_4 (.J(_1), .clk(q2), .K(_1), .Q(q3), .Qn(j_k_ff_4_qn), .preset(or_1_out));  // open: en, reset
  J_K_Flip_Flop j_k_ff_5 (.J(_1), .clk(q3), .K(_1), .Q(q4), .Qn(j_k_ff_5_qn), .preset(or_1_out));  // open: en, reset

  // Notes on the sheet:
  //   qnot
  //   q1not
  //   q2not
  //   q3not
  //   q4not
endmodule
