// Logisim project Exercicio04.circ as structural Verilog: 1 circuit, main circuit main
module main (
  input  _1,
  input  pulse,
  input  CLR,
  output q4,
  output q3,
  output q2,
  output q1,
  output q
);

  wire j_k_ff_1_qn, j_k_ff_2_qn, j_k_ff_3_qn, j_k_ff_4_qn, nand_1_out, nand_2_out, not_1_out, not_2_out,
       not_3_out;

  nand nand_1 (nand_1_out, not_1_out, q1, not_2_out, q3, not_3_out);
  J_K_Flip_Flop j_k_ff_1 (
    .J(_1), .clk(pulse), .K(_1), .Q(q), .Qn(j_k_ff_1_qn), .reset(nand_2_out));  // open: preset, en
  nand nand_2 (nand_2_out, CLR, nand_1_out);
  not not_1 (not_1_out, q);
  not not_2 (not_2_out, q2);
  not not_3 (not_3_out, q4);
  J_K_Flip_Flop j_k_ff_2 (
    .J(_1), .clk(j_k_ff_1_qn), .K(_1), .Q(q1), .Qn(j_k_ff_2_qn), .reset(nand_2_out));  // open: preset, en
  J_K_Flip_Flop j_k_ff_3 (
    .J(_1), .clk(j_k_ff_2_qn), .K(_1), .Q(q2), .Qn(j_k_ff_3_qn), .reset(nand_2_out));  // open: preset, en
  J_K_Flip_Flop j_k_ff_4 (
    .J(_1), .clk(j_k_ff_3_qn), .K(_1), .Q(q3), .Qn(j_k_ff_4_qn), .reset(nand_2_out));  // open: preset, en
  J_K_Flip_Flop j_k_ff_5 (.J(_1), .clk(j_k_ff_4_qn), .K(_1), .Q(q4), .reset(nand_2_out));  // open: Qn, preset, en

  // Notes on the sheet:
  //   q
  //   q1
  //   q2
  //   q3
  //   q4
endmodule
