// Logisim project Exercicio05.circ as structural Verilog: 1 circuit, main circuit main
module main (
  input  pulse,
  input  CLR,
  output q3,
  output q2,
  output q1,
  output q
);

  wire and_1_out, or_1_out, t_ff_2_qn, t_ff_3_qn, t_ff_4_qn;

  or or_1 (or_1_out, CLR, and_1_out);
  and and_1 (and_1_out, q3, t_ff_2_qn, t_ff_3_qn, t_ff_4_qn);
  T_Flip_Flop t_ff_1 (.clk(t_ff_2_qn), .T(t_ff_2_qn), .Q(q3), .reset(or_1_out));  // open: Qn, preset, en
  T_Flip_Flop t_ff_2 (.clk(t_ff_3_qn), .T(t_ff_3_qn), .Q(q2), .Qn(t_ff_2_qn), .reset(or_1_out));  // open: preset, en
  T_Flip_Flop t_ff_3 (.clk(t_ff_4_qn), .T(t_ff_4_qn), .Q(q1), .Qn(t_ff_3_qn), .reset(or_1_out));  // open: preset, en
  T_Flip_Flop t_ff_4 (.clk(pulse), .T(pulse), .Q(q), .Qn(t_ff_4_qn), .reset(or_1_out));  // open: preset, en

  // Notes on the sheet:
  //   q2not
  //   q1not
  //   qnot
endmodule
