// Logisim project Exercicio001.circ as structural Verilog: 1 circuit, main circuit main
module main (
  input  data,
  input  CLR,
  output [4:0] saida
);

  wire CLK_out;

  Clock CLK (.out(CLK_out));
  J_K_Flip_Flop A (.J(data), .clk(saida[3]), .K(data), .Qn(saida[4]), .reset(CLR));  // open: Q, preset, en
  J_K_Flip_Flop B (.J(data), .clk(saida[2]), .K(data), .Qn(saida[3]), .reset(CLR));  // open: Q, preset, en
  J_K_Flip_Flop C (.J(data), .clk(saida[1]), .K(data), .Qn(saida[2]), .reset(CLR));  // open: Q, preset, en
  J_K_Flip_Flop D (.J(data), .clk(saida[0]), .K(data), .Qn(saida[1]), .reset(CLR));  // open: Q, preset, en
  J_K_Flip_Flop E (.J(data), .clk(CLK_out), .K(data), .Qn(saida[0]), .reset(CLR));  // open: Q, preset, en

  // Notes on the sheet:
  //   J = data
  //   K = data
  //   CLK E = CLK
  //   CLK D = ~QE
  //   CLK C = ~QD
  //   CLK B = ~QC
  //   CLK A = ~QB
  //   ~QB
  //   data
  //   ~QC
  //   data
  //   Contador Assincrono Descrescente para 5 bits
  //   ~QD
  //   data
  //   saida =  ~QA | ~QB | ~QC | ~QD | ~QE
  //   ~QE
  //   data
  //   data
endmodule
