// Logisim project Exercicio002.circ as structural Verilog: 1 circuit, main circuit main
module main (
  input  CLR,
  output [4:0] saida
);

  wire B_q, C_q, CLK_out, D_q, E_q;

  Clock CLK (.out(CLK_out));
  J_K_Flip_Flop A (.J(1'b1), .clk(B_q), .K(1'b1), .Qn(saida[4]), .reset(CLR));  // open: Q, preset, en
  J_K_Flip_Flop B (.J(1'b1), .clk(C_q), .K(1'b1), .Q(B_q), .Qn(saida[3]), .reset(CLR));  // open: preset, en
  J_K_Flip_Flop C (.J(1'b1), .clk(D_q), .K(1'b1), .Q(C_q), .Qn(saida[2]), .reset(CLR));  // open: preset, en
  J_K_Flip_Flop D (.J(1'b1), .clk(E_q), .K(1'b1), .Q(D_q), .Qn(saida[1]), .reset(CLR));  // open: preset, en
  J_K_Flip_Flop E (.J(1'b1), .clk(CLK_out), .K(1'b1), .Q(E_q), .Qn(saida[0]), .reset(CLR));  // open: preset, en

  // Notes on the sheet:
  //   BITS =  B4 |  B3 |  B2 |  B1|  B0
  //   saida = ~QA | ~QB | ~QC | ~QD | ~QE
endmodule
