// Logisim project Exercicio003.circ as structural Verilog: 1 circuit, main circuit main
module main (
  input  Data,
  input  CLR,
  output [4:0] saida
);

  wire A_qn, B_qn, C_qn, CLK_out, D_qn, E_qn, F_out, G_out, N0_out, N1_out, N2_out, N3_out;

  Clock CLK (.out(CLK_out));
  not N0 (N0_out, Data);
  // Probe on saida
  J_K_Flip_Flop A (
    .J(Data), .clk(CLK_out), .K(Data), .Q(saida[0]), .Qn(A_qn), .preset(F_out), .reset(CLR));  // open: en
  or F (F_out, N0_out, G_out);
  and G (G_out, N1_out, B_qn, N2_out, D_qn, N3_out);
  J_K_Flip_Flop B (
    .J(Data), .clk(saida[0]), .K(Data), .Q(saida[1]), .Qn(B_qn), .preset(F_out), .reset(CLR));  // open: en
  not N1 (N1_out, A_qn);
  J_K_Flip_Flop C (
    .J(Data), .clk(saida[1]), .K(Data), .Q(saida[2]), .Qn(C_qn), .preset(F_out), .reset(CLR));  // open: en
  not N2 (N2_out, C_qn);
  J_K_Flip_Flop D (
    .J(Data), .clk(saida[2]), .K(Data), .Q(saida[3]), .Qn(D_qn), .preset(F_out), .reset(CLR));  // open: en
  J_K_Flip_Flop E (
    .J(Data), .clk(saida[3]), .K(Data), .Q(saida[4]), .Qn(E_qn), .preset(F_out), .reset(CLR));  // open: en
  not N3 (N3_out, E_qn);

  // Notes on the sheet:
  //   n0
  //   qnota
  //   pst
  //   g
  //   n1
  //   qa
  //   qnotb
  //   qb
  //   qc
  //   qnotc
  //   n2
  //   saida = ~QE | ~QD | ~QC | ~QB | ~QA
  //   qnotd
  //   qd
  //   qe
  //   qnote
  //   n3
endmodule
