// Logisim project Exercicio004.circ as structural Verilog: 1 circuit, main circuit main
module main (
  input  Data,
  input  CLR,
  output [4:0] saida
);

  wire A_qn, B_qn, C_qn, CLK_out, D_qn, F_out, G_out, N0_out, N1_out, N2_out;

  // Probe on saida
  Clock CLK (.out(CLK_out));
  nand F (F_out, CLR, G_out);
  nand G (G_out, N0_out, saida[1], N1_out, saida[3], N2_out);
  J_K_Flip_Flop A (.J(Data), .clk(CLK_out), .K(Data), .Q(saida[0]), .Qn(A_qn), .reset(F_out));  // open: preset, en
  not N0 (N0_out, saida[0]);
  J_K_Flip_Flop B (.J(Data), .clk(A_qn), .K(Data), .Q(saida[1]), .Qn(B_qn), .reset(F_out));  // open: preset, en
  J_K_Flip_Flop C (.J(Data), .clk(B_qn), .K(Data), .Q(saida[2]), .Qn(C_qn), .reset(F_out));  // open: preset, en
  not N1 (N1_out, saida[2]);
  J_K_Flip_Flop D (.J(Data), .clk(C_qn), .K(Data), .Q(saida[3]), .Qn(D_qn), .reset(F_out));  // open: preset, en
  J_K_Flip_Flop E (.J(Data), .clk(D_qn), .K(Data), .Q(saida[4]), .reset(F_out));  // open: Qn, preset, en
  not N2 (N2_out, saida[4]);

  // Notes on the sheet:
  //   clr
  //   g
  //   q0
  //   n0
  //   q1
  //   saida = QE | QD | QC | QB | QA
  //   q2
  //   n1
  //   QNOT = propaga o CLK
  //   q3
  //   q4
  //   n2
endmodule
