// Logisim project Exercicio005.circ as structural Verilog: 1 circuit, main circuit main
module main (
  input  CLR,
  output [3:0] saida
);

  wire B_qn, C_qn, CLK_out, D_qn, E_out, F_out;

  Clock CLK (.out(CLK_out));
  // Probe on saida
  or E (E_out, CLR, F_out);
  and F (F_out, saida[3], B_qn, C_qn, D_qn);
  T_Flip_Flop B (.clk(C_qn), .T(C_qn), .Q(saida[2]), .Qn(B_qn), .reset(E_out));  // open: preset, en
  T_Flip_Flop A (.clk(B_qn), .T(B_qn), .Q(saida[3]), .reset(E_out));  // open: Qn, preset, en
  T_Flip_Flop C (.clk(D_qn), .T(D_qn), .Q(saida[1]), .Qn(C_qn), .reset(E_out));  // open: preset, en
  T_Flip_Flop D (.clk(CLK_out), .T(CLK_out), .Q(saida[0]), .Qn(D_qn), .reset(E_out));  // open: preset, en

  // Notes on the sheet:
  //   qnot2
  //   w2
  //   w1
  //   qnot1
  //   w2
  //   q3
  //   qnot2
  //   saida = QA | QB | QC | QD
  //   w2
  //   qnot1
  //   qnot0
  //   w2
  //   qnot0
endmodule
