// Logisim project Exercicio006.circ as structural Verilog: 1 circuit, main circuit main
module main (
  input  pulse,
  input  CLR,
  output [4:0] out_3
);

  wire A_qn, B_qn, C_qn, CLK_out, D_qn, F_out, N0_out;

  Clock CLK (.out(CLK_out));
  // Probe on out_3
  or F (F_out, pulse, out_3[0]);
  J_K_Flip_Flop A (.J(F_out), .clk(CLK_out), .K(N0_out), .Q(out_3[4]), .Qn(A_qn), .reset(CLR));  // open: preset, en
  not N0 (N0_out, F_out);
  J_K_Flip_Flop B (.J(out_3[4]), .clk(CLK_out), .K(A_qn), .Q(out_3[3]), .Qn(B_qn), .reset(CLR));  // open: preset, en
  J_K_Flip_Flop C (.J(out_3[3]), .clk(CLK_out), .K(B_qn), .Q(out_3[2]), .Qn(C_qn), .reset(CLR));  // open: preset, en
  J_K_Flip_Flop D (.J(out_3[2]), .clk(CLK_out), .K(C_qn), .Q(out_3[1]), .Qn(D_qn), .reset(CLR));  // open: preset, en
  J_K_Flip_Flop E (.J(out_3[1]), .clk(CLK_out), .K(D_qn), .Q(out_3[0]), .reset(CLR));  // open: Qn, preset, en

  // Notes on the sheet:
  //   f
  //   n
  //   qa
  //   qb
  //   saida = QA | QB | QC | QD | QE
  //   qc
  //   qd
  //   qe
  //   qe
endmodule
