// Logisim project Exercicio01.circ as structural Verilog: 1 circuit, main circuit main
module main (
  input  in_1,
  input  in_2,
  input  in_3,
  output out_4,
  output out_5,
  output out_6,
  output out_7,
  output out_8
);

  J_K_Flip_Flop j_k_ff_1 (.J(in_1), .clk(out_5), .K(in_1), .Qn(out_4), .reset(in_2));  // open: Q, preset, en
  J_K_Flip_Flop j_k_ff_2 (.J(in_1), .clk(out_6), .K(in_1), .Qn(out_5), .reset(in_2));  // open: Q, preset, en
  J_K_Flip_Flop j_k_ff_3 (.J(in_1), .clk(out_7), .K(in_1), .Qn(out_6), .reset(in_2));  // open: Q, preset, en
  J_K_Flip_Flop j_k_ff_4 (.J(in_1), .clk(out_8), .K(in_1), .Qn(out_7), .reset(in_2));  // open: Q, preset, en
  J_K_Flip_Flop j_k_ff_5 (.J(in_1), .clk(in_3), .K(in_1), .Qn(out_8), .reset(in_2));  // open: Q, preset, en

  // Notes on the sheet:
  //   Lucas Siqueira Chagas
endmodule
