// Logisim project Circuitos.circ as structural Verilog: 8 circuits, main circuit main
module main (
  input  CLK,
  input  CLK_2,
  input  CLK_3,
  input  [3:0] IN,
  input  [3:0] IN_2,
  input  [7:0] IN_3,
  input  R_W,
  input  R_W_2,
  input  R_W_3,
  input  ADDRESS,
  input  ADDRESS_2,
  input  ADDRESS_3,
  input  CLEAR,
  input  CLEAR_2,
  input  CLEAR_3,
  input  CLK_4,
  input  CLK_5,
  input  CLK_6,
  input  [15:0] IN_4,
  input  [7:0] IN_5,
  input  [7:0] IN_6,
  input  R_W_4,
  input  R_W_5,
  input  R_W_6,
  input  ADDRESS_4,
  input  [2:0] ADDRESS_5,
  input  ADDRESS_6,
  input  CLEAR_4,
  input  CLEAR_5,
  input  CLEAR_6,
  input  CLK_7,
  input  [7:0] IN_7,
  input  R_W_7,
  input  [1:0] ADDRESS_7,
  input  CLEAR_7,
  output [3:0] OUT,
  output [3:0] OUT_2,
  output [7:0] OUT_3,
  output [7:0] OUT_4,
  output [7:0] OUT_5,
  output [15:0] OUT_6,
  output [7:0] OUT_7
);

  memory1x4 RAM (.CLK(CLK), .R_W(R_W), .ADDRESS(ADDRESS), .IN(IN), .OUT(OUT), .CLR(CLEAR));
  memory2x8 RAM_2 (.CLK(CLK_4), .R_W(R_W_4), .ADRESS(ADDRESS_4), .IN(IN_5), .OUT(OUT_4), .CLR(CLEAR_4));
  memory4x8 RAM_3 (.CLK(CLK_7), .R_W(R_W_7), .ADDRESS(ADDRESS_7), .IN(IN_7), .OUT(OUT_7), .CLR(CLEAR_7));
  memory2x4 RAM_4 (.CLK(CLK_2), .R_W(R_W_2), .ADRESS(ADDRESS_2), .IN(IN_2), .OUT(OUT_2), .CLR(CLEAR_2));
  memory8x8 RAM_5 (.CLK(CLK_5), .R_W(R_W_5), .ADDRESS(ADDRESS_5), .IN(IN_6), .out_6(OUT_5), .CLR(CLEAR_5));
  memory1x8 RAM_6 (.CLK(CLK_3), .R_W(R_W_3), .ADDRESS(ADDRESS_3), .IN(IN_3), .OUT(OUT_3), .CLR(CLEAR_3));
  memory1x16 RAM_7 (.CLK(CLK_6), .R_W(R_W_6), .ADDRESS(ADDRESS_6), .IN(IN_4), .OUT(OUT_6), .CLR(CLEAR_6));

  // Notes on the sheet:
  //   Exercício 1
  //   Exercício 4
  //   Exercício 7
  //   Exercício 2
  //   Exercício 5
  //   Exercício 3
  //   Exercício 6
endmodule

// 1x4
module memory1x4 (
  input  CLK,
  input  [3:0] IN,
  input  R_W,
  input  ADDRESS,
  input  CLR,
  output [3:0] OUT
);

  wire and_1_out, not_1_out, not_2_out, not_3_out, not_4_out;
  wire [3:0] j_k_ff_4_q;

  and and_1 (and_1_out, CLK, R_W, ADDRESS);
  J_K_Flip_Flop j_k_ff_1 (
    .J(IN[3]), .clk(and_1_out), .K(not_1_out), .Q(j_k_ff_4_q[3]), .reset(CLR));  // open: Qn, preset, en
  not not_1 (not_1_out, IN[3]);
  not not_2 (not_2_out, IN[2]);
  J_K_Flip_Flop j_k_ff_2 (
    .J(IN[2]), .clk(and_1_out), .K(not_2_out), .Q(j_k_ff_4_q[2]), .reset(CLR));  // open: Qn, preset, en
  J_K_Flip_Flop j_k_ff_3 (
    .J(IN[1]), .clk(and_1_out), .K(not_3_out), .Q(j_k_ff_4_q[1]), .reset(CLR));  // open: Qn, preset, en
  not not_3 (not_3_out, IN[1]);
  not not_4 (not_4_out, IN[0]);
  J_K_Flip_Flop j_k_ff_4 (
    .J(IN[0]), .clk(and_1_out), .K(not_4_out), .Q(j_k_ff_4_q[0]), .reset(CLR));  // open: Qn, preset, en
  assign OUT = j_k_ff_4_q & {4{ADDRESS}};  // AND_Gate and_2, 4 bits wide
endmodule

// 2X4
module memory2x4 (
  input  CLK,
  input  R_W,
  input  ADRESS,
  input  [3:0] IN,
  input  CLR,
  output [3:0] OUT
);

  wire demultiplexer_1_out0, demultiplexer_1_out1;
  wire [3:0] memory1x4_1_out, memory1x4_2_out;

  Demultiplexer #(.enable("false")) demultiplexer_1 (
    .out0(demultiplexer_1_out0), .out1(demultiplexer_1_out1), .in(1'b1), .sel(ADRESS));
  memory1x4 memory1x4_1 (
    .CLK(CLK), .R_W(R_W), .ADDRESS(demultiplexer_1_out0), .IN(IN), .OUT(memory1x4_1_out), .CLR(CLR));
  memory1x4 memory1x4_2 (
    .CLK(CLK), .R_W(R_W), .ADDRESS(demultiplexer_1_out1), .IN(IN), .OUT(memory1x4_2_out), .CLR(CLR));
  Multiplexer #(.width(4), .enable("false")) multiplexer_1 (
    .in0(memory1x4_1_out), .in1(memory1x4_2_out), .out(OUT), .sel(ADRESS));
endmodule

// 1X8
module memory1x8 (
  input  CLK,
  input  R_W,
  input  ADDRESS,
  input  [7:0] IN,
  input  CLR,
  output [7:0] OUT
);

  memory1x4 memory1x4_1 (.CLK(CLK), .R_W(R_W), .ADDRESS(ADDRESS), .IN(IN[3:0]), .OUT(OUT[3:0]), .CLR(CLR));
  memory1x4 memory1x4_2 (.CLK(CLK), .R_W(R_W), .ADDRESS(ADDRESS), .IN(IN[7:4]), .OUT(OUT[7:4]), .CLR(CLR));
endmodule

// 2X8
module memory2x8 (
  input  CLK,
  input  R_W,
  input  ADRESS,
  input  [7:0] IN,
  input  CLR,
  output [7:0] OUT
);

  wire demultiplexer_1_out0, demultiplexer_1_out1;
  wire [3:0] memory2x4_1_out, memory2x4_2_out, memory2x4_3_out, memory2x4_4_out;

  Demultiplexer #(.enable("false")) demultiplexer_1 (
    .out0(demultiplexer_1_out0), .out1(demultiplexer_1_out1), .in(1'b1), .sel(ADRESS));
  memory2x4 memory2x4_1 (
    .CLK(CLK), .R_W(R_W), .ADRESS(demultiplexer_1_out0), .IN(IN[3:0]), .OUT(memory2x4_1_out), .CLR(CLR));
  memory2x4 memory2x4_2 (
    .CLK(CLK), .R_W(R_W), .ADRESS(demultiplexer_1_out0), .IN(IN[7:4]), .OUT(memory2x4_2_out), .CLR(CLR));
  memory2x4 memory2x4_3 (
    .CLK(CLK), .R_W(R_W), .ADRESS(demultiplexer_1_out1), .IN(IN[3:0]), .OUT(memory2x4_3_out), .CLR(CLR));
  memory2x4 memory2x4_4 (
    .CLK(CLK), .R_W(R_W), .ADRESS(demultiplexer_1_out1), .IN(IN[7:4]), .OUT(memory2x4_4_out), .CLR(CLR));
  Multiplexer #(.width(8), .enable("false")) multiplexer_1 (
    .in0({memory2x4_2_out, memory2x4_1_out}), .in1({memory2x4_4_out, memory2x4_3_out}), .out(OUT),
    .sel(ADRESS));
endmodule

// 8x8
module memory8x8 (
  input  CLK,
  input  R_W,
  input  [2:0] ADDRESS,
  input  [7:0] IN,
  input  CLR,
  output [7:0] out_6
);

  wire demultiplexer_1_out0, demultiplexer_1_out1, demultiplexer_1_out2, demultiplexer_1_out3,
       demultiplexer_1_out4, demultiplexer_1_out5, demultiplexer_1_out6, demultiplexer_1_out7;
  wire [7:0] memory1x8_1_out, memory1x8_2_out, memory1x8_3_out, memory1x8_4_out, memory1x8_5_out,
       memory1x8_6_out, memory1x8_7_out, memory1x8_8_out;

  Demultiplexer #(.select(3), .enable("false")) demultiplexer_1 (
    .out0(demultiplexer_1_out0), .out1(demultiplexer_1_out1), .out2(demultiplexer_1_out2),
    .out3(demultiplexer_1_out3), .out4(demultiplexer_1_out4), .out5(demultiplexer_1_out5),
    .out6(demultiplexer_1_out6), .out7(demultiplexer_1_out7), .in(1'b1), .sel(ADDRESS));
  memory1x8 memory1x8_1 (
    .CLK(CLK), .R_W(R_W), .ADDRESS(demultiplexer_1_out0), .IN(IN), .OUT(memory1x8_1_out), .CLR(CLR));
  memory1x8 memory1x8_2 (
    .CLK(CLK), .R_W(R_W), .ADDRESS(demultiplexer_1_out1), .IN(IN), .OUT(memory1x8_2_out), .CLR(CLR));
  memory1x8 memory1x8_3 (
    .CLK(CLK), .R_W(R_W), .ADDRESS(demultiplexer_1_out2), .IN(IN), .OUT(memory1x8_3_out), .CLR(CLR));
  memory1x8 memory1x8_4 (
    .CLK(CLK), .R_W(R_W), .ADDRESS(demultiplexer_1_out3), .IN(IN), .OUT(memory1x8_4_out), .CLR(CLR));
  memory1x8 memory1x8_5 (
    .CLK(CLK), .R_W(R_W), .ADDRESS(demultiplexer_1_out4), .IN(IN), .OUT(memory1x8_5_out), .CLR(CLR));
  memory1x8 memory1x8_6 (
    .CLK(CLK), .R_W(R_W), .ADDRESS(demultiplexer_1_out5), .IN(IN), .OUT(memory1x8_6_out), .CLR(CLR));
  memory1x8 memory1x8_7 (
    .CLK(CLK), .R_W(R_W), .ADDRESS(demultiplexer_1_out6), .IN(IN), .OUT(memory1x8_7_out), .CLR(CLR));
  memory1x8 memory1x8_8 (
    .CLK(CLK), .R_W(R_W), .ADDRESS(demultiplexer_1_out7), .IN(IN), .OUT(memory1x8_8_out), .CLR(CLR));
  Multiplexer #(.select(3), .width(8), .enable("false")) multiplexer_1 (
    .in0(memory1x8_1_out), .in1(memory1x8_2_out), .in2(memory1x8_3_out), .in3(memory1x8_4_out),
    .in4(memory1x8_5_out), .in5(memory1x8_6_out), .in6(memory1x8_7_out), .in7(memory1x8_8_out), .out(out_6),
    .sel(ADDRESS));
endmodule

// 1X16
module memory1x16 (
  input  CLK,
  input  R_W,
  input  ADDRESS,
  input  [15:0] IN,
  input  CLR,
  output [15:0] OUT
);

  memory1x4 memory1x4_1 (.CLK(CLK), .R_W(R_W), .ADDRESS(ADDRESS), .IN(IN[3:0]), .OUT(OUT[3:0]), .CLR(CLR));
  memory1x4 memory1x4_2 (.CLK(CLK), .R_W(R_W), .ADDRESS(ADDRESS), .IN(IN[7:4]), .OUT(OUT[7:4]), .CLR(CLR));
  memory1x4 memory1x4_3 (.CLK(CLK), .R_W(R_W), .ADDRESS(ADDRESS), .IN(IN[11:8]), .OUT(OUT[11:8]), .CLR(CLR));
  memory1x4 memory1x4_4 (.CLK(CLK), .R_W(R_W), .ADDRESS(ADDRESS), .IN(IN[15:12]), .OUT(OUT[15:12]), .CLR(CLR));
endmodule

// 4X8
module memory4x8 (
  input  CLK,
  input  R_W,
  input  [1:0] ADDRESS,
  input  [7:0] IN,
  input  CLR,
  output [7:0] OUT
);

  wire demultiplexer_1_out0, demultiplexer_1_out1, demultiplexer_1_out2, demultiplexer_1_out3;
  wire [7:0] memory1x8_1_out, memory1x8_2_out, memory1x8_3_out, memory1x8_4_out;

  Demultiplexer #(.select(2), .enable("false")) demultiplexer_1 (
    .out0(demultiplexer_1_out0), .out1(demultiplexer_1_out1), .out2(demultiplexer_1_out2),
    .out3(demultiplexer_1_out3), .in(1'b1), .sel(ADDRESS));
  memory1x8 memory1x8_1 (
    .CLK(CLK), .R_W(R_W), .ADDRESS(demultiplexer_1_out0), .IN(IN), .OUT(memory1x8_1_out), .CLR(CLR));
  memory1x8 memory1x8_2 (
    .CLK(CLK), .R_W(R_W), .ADDRESS(demultiplexer_1_out1), .IN(IN), .OUT(memory1x8_2_out), .CLR(CLR));
  memory1x8 memory1x8_3 (
    .CLK(CLK), .R_W(R_W), .ADDRESS(demultiplexer_1_out2), .IN(IN), .OUT(memory1x8_3_out), .CLR(CLR));
  memory1x8 memory1x8_4 (
    .CLK(CLK), .R_W(R_W), .ADDRESS(demultiplexer_1_out3), .IN(IN), .OUT(memory1x8_4_out), .CLR(CLR));
  Multiplexer #(.select(2), .width(8), .enable("false")) multiplexer_1 (
    .in0(memory1x8_1_out), .in1(memory1x8_2_out), .in2(memory1x8_3_out), .in3(memory1x8_4_out), .out(OUT),
    .sel(ADDRESS));
endmodule
