// Logisim project Circuitos.circ as structural Verilog: 7 circuits, main circuit Exercicio 01
// 1x4
module Exercicio_01 (
  input  Clock,
  input  [3:0] IN,
  input  Read_Write,
  input  Adress,
  input  Clear,
  output [3:0] OUT
);

  wire and_1_out, not_1_out, not_2_out, not_3_out, not_4_out;
  wire [3:0] j_k_ff_4_q;

  and and_1 (and_1_out, Clock, Read_Write, Adress);
  J_K_Flip_Flop j_k_ff_1 (
    .J(IN[3]), .clk(and_1_out), .K(not_1_out), .Q(j_k_ff_4_q[3]), .reset(Clear));  // open: Qn, preset, en
  not not_1 (not_1_out, IN[3]);
  not not_2 (not_2_out, IN[2]);
  J_K_Flip_Flop j_k_ff_2 (
    .J(IN[2]), .clk(and_1_out), .K(not_2_out), .Q(j_k_ff_4_q[2]), .reset(Clear));  // open: Qn, preset, en
  J_K_Flip_Flop j_k_ff_3 (
    .J(IN[1]), .clk(and_1_out), .K(not_3_out), .Q(j_k_ff_4_q[1]), .reset(Clear));  // open: Qn, preset, en
  not not_3 (not_3_out, IN[1]);
  not not_4 (not_4_out, IN[0]);
  J_K_Flip_Flop j_k_ff_4 (
    .J(IN[0]), .clk(and_1_out), .K(not_4_out), .Q(j_k_ff_4_q[0]), .reset(Clear));  // open: Qn, preset, en
  assign OUT = j_k_ff_4_q & {4{Adress}};  // AND_Gate and_2, 4 bits wide

  // Notes on the sheet:
  //   Alvaro Henrique de Araujo Rungue
endmodule

// 2x4
module Exercicio_02 (
  input  Clock,
  input  Read_Write,
  input  Adress,
  input  [3:0] IN,
  input  Clear,
  output [3:0] OUT
);

  wire demultiplexer_1_out0, demultiplexer_1_out1;
  wire [3:0] exercicio_01_1_out, exercicio_01_2_out;

  Demultiplexer #(.enable("false")) demultiplexer_1 (
    .out0(demultiplexer_1_out0), .out1(demultiplexer_1_out1), .in(1'b1), .sel(Adress));
  Exercicio_01 exercicio_01_1 (
    .Clock(Clock), .Read_Write(Read_Write), .Adress(demultiplexer_1_out0), .Clear(Clear), .IN(IN),
    .OUT(exercicio_01_1_out));
  Exercicio_01 exercicio_01_2 (
    .Clock(Clock), .Read_Write(Read_Write), .Adress(demultiplexer_1_out1), .Clear(Clear), .IN(IN),
    .OUT(exercicio_01_2_out));
  Multiplexer #(.width(4), .enable("false")) multiplexer_1 (
    .in0(exercicio_01_1_out), .in1(exercicio_01_2_out), .out(OUT), .sel(Adress));

  // Notes on the sheet:
  //   Alvaro Henrique de Araujo Rungue
endmodule

// 1x8
module Exercicio_03 (
  input  Clock,
  input  Read_Write,
  input  Adress,
  input  [7:0] IN,
  input  Clear,
  output [7:0] OUT
);

  Exercicio_01 exercicio_01_1 (
    .Clock(Clock), .Read_Write(Read_Write), .Adress(Adress), .Clear(Clear), .IN(IN[3:0]), .OUT(OUT[3:0]));
  Exercicio_01 exercicio_01_2 (
    .Clock(Clock), .Read_Write(Read_Write), .Adress(Adress), .Clear(Clear), .IN(IN[7:4]), .OUT(OUT[7:4]));

  // Notes on the sheet:
  //   Alvaro Henrique de Araujo Rungue
endmodule

module Exercicio_04 (
  input  Clock,
  input  Read_Write,
  input  Adress,
  input  [7:0] IN,
  input  Clear,
  output [7:0] OUT
);

  wire demultiplexer_1_out0, demultiplexer_1_out1;
  wire [3:0] exercicio_02_1_out, exercicio_02_2_out, exercicio_02_3_out, exercicio_02_4_out;

  Demultiplexer #(.enable("false")) demultiplexer_1 (
    .out0(demultiplexer_1_out0), .out1(demultiplexer_1_out1), .in(1'b1), .sel(Adress));
  Exercicio_02 exercicio_02_1 (
    .Clock(Clock), .Read_Write(Read_Write), .Adress(demultiplexer_1_out0), .Clear(Clear), .IN(IN[3:0]),
    .OUT(exercicio_02_1_out));
  Exercicio_02 exercicio_02_2 (
    .Clock(Clock), .Read_Write(Read_Write), .Adress(demultiplexer_1_out0), .Clear(Clear), .IN(IN[7:4]),
    .OUT(exercicio_02_2_out));
  Exercicio_02 exercicio_02_3 (
    .Clock(Clock), .Read_Write(Read_Write), .Adress(demultiplexer_1_out1), .Clear(Clear), .IN(IN[3:0]),
    .OUT(exercicio_02_3_out));
  Exercicio_02 exercicio_02_4 (
    .Clock(Clock), .Read_Write(Read_Write), .Adress(demultiplexer_1_out1), .Clear(Clear), .IN(IN[7:4]),
    .OUT(exercicio_02_4_out));
  Multiplexer #(.width(8), .enable("false")) multiplexer_1 (
    .in0({exercicio_02_2_out, exercicio_02_1_out}), .in1({exercicio_02_4_out, exercicio_02_3_out}),
    .out(OUT), .sel(Adress));

  // Notes on the sheet:
  //   Alvaro Henrique de Araujo Rungue
endmodule

module Exercicio_05 (
  input  Clock,
  input  Read_Write,
  input  [2:0] Adress,
  input  [7:0] IN,
  input  Clear,
  output [7:0] out_6
);

  wire demultiplexer_1_out0, demultiplexer_1_out1, demultiplexer_1_out2, demultiplexer_1_out3,
       demultiplexer_1_out4, demultiplexer_1_out5, demultiplexer_1_out6, demultiplexer_1_out7;
  wire [7:0] exercicio_03_1_out, exercicio_03_2_out, exercicio_03_3_out, exercicio_03_4_out,
       exercicio_03_5_out, exercicio_03_6_out, exercicio_03_7_out, exercicio_03_8_out;

  Demultiplexer #(.select(3), .enable("false")) demultiplexer_1 (
    .out0(demultiplexer_1_out0), .out1(demultiplexer_1_out1), .out2(demultiplexer_1_out2),
    .out3(demultiplexer_1_out3), .out4(demultiplexer_1_out4), .out5(demultiplexer_1_out5),
    .out6(demultiplexer_1_out6), .out7(demultiplexer_1_out7), .in(1'b1), .sel(Adress));
  Exercicio_03 exercicio_03_1 (
    .Clock(Clock), .Read_Write(Read_Write), .Adress(demultiplexer_1_out0), .Clear(Clear), .IN(IN),
    .OUT(exercicio_03_1_out));
  Exercicio_03 exercicio_03_2 (
    .Clock(Clock), .Read_Write(Read_Write), .Adress(demultiplexer_1_out1), .Clear(Clear), .IN(IN),
    .OUT(exercicio_03_2_out));
  Exercicio_03 exercicio_03_3 (
    .Clock(Clock), .Read_Write(Read_Write), .Adress(demultiplexer_1_out2), .Clear(Clear), .IN(IN),
    .OUT(exercicio_03_3_out));
  Exercicio_03 exercicio_03_4 (
    .Clock(Clock), .Read_Write(Read_Write), .Adress(demultiplexer_1_out3), .Clear(Clear), .IN(IN),
    .OUT(exercicio_03_4_out));
  Exercicio_03 exercicio_03_5 (
    .Clock(Clock), .Read_Write(Read_Write), .Adress(demultiplexer_1_out4), .Clear(Clear), .IN(IN),
    .OUT(exercicio_03_5_out));
  Exercicio_03 exercicio_03_6 (
    .Clock(Clock), .Read_Write(Read_Write), .Adress(demultiplexer_1_out5), .Clear(Clear), .IN(IN),
    .OUT(exercicio_03_6_out));
  Exercicio_03 exercicio_03_7 (
    .Clock(Clock), .Read_Write(Read_Write), .Adress(demultiplexer_1_out6), .Clear(Clear), .IN(IN),
    .OUT(exercicio_03_7_out));
  Exercicio_03 exercicio_03_8 (
    .Clock(Clock), .Read_Write(Read_Write), .Adress(demultiplexer_1_out7), .Clear(Clear), .IN(IN),
    .OUT(exercicio_03_8_out));
  Multiplexer #(.select(3), .width(8), .enable("false")) multiplexer_1 (
    .in0(exercicio_03_1_out), .in1(exercicio_03_2_out), .in2(exercicio_03_3_out), .in3(exercicio_03_4_out),
    .in4(exercicio_03_5_out), .in5(exercicio_03_6_out), .in6(exercicio_03_7_out), .in7(exercicio_03_8_out),
    .out(out_6), .sel(Adress));

  // Notes on the sheet:
  //   Alvaro Henrique de Aruajo Rungue
endmodule

module Exercicio_06 (
  input  Clock,
  input  Read_Write,
  input  Adress,
  input  [15:0] IN,
  input  Clear,
  output [15:0] OUT
);

  Exercicio_03 exercicio_03_1 (
    .Clock(Clock), .Read_Write(Read_Write), .Adress(Adress), .Clear(Clear), .IN(IN[7:0]), .OUT(IN[15:8]));
  Exercicio_03 exercicio_03_2 (
    .Clock(Clock), .Read_Write(Read_Write), .Adress(Adress), .Clear(Clear), .IN(IN[15:8]), .OUT(OUT[15:8]));

  assign OUT[7:0] = IN[15:8];

  // Notes on the sheet:
  //   Alvaro Henrique de Araujo Rungue
endmodule

module Exercicio_07 (
  input  Clock,
  input  Read_Write,
  input  [1:0] Adress,
  input  [7:0] IN,
  input  Clear,
  output [7:0] OUT
);

  wire demultiplexer_1_out0, demultiplexer_1_out1, demultiplexer_1_out2, demultiplexer_1_out3;
  wire [7:0] exercicio_03_1_out, exercicio_03_2_out, exercicio_03_3_out, exercicio_03_4_out;

  Demultiplexer #(.select(2), .enable("false")) demultiplexer_1 (
    .out0(demultiplexer_1_out0), .out1(demultiplexer_1_out1), .out2(demultiplexer_1_out2),
    .out3(demultiplexer_1_out3), .in(1'b1), .sel(Adress));
  Exercicio_03 exercicio_03_1 (
    .Clock(Clock), .Read_Write(Read_Write), .Adress(demultiplexer_1_out0), .Clear(Clear), .IN(IN),
    .OUT(exercicio_03_1_out));
  Exercicio_03 exercicio_03_2 (
    .Clock(Clock), .Read_Write(Read_Write), .Adress(demultiplexer_1_out1), .Clear(Clear), .IN(IN),
    .OUT(exercicio_03_2_out));
  Exercicio_03 exercicio_03_3 (
    .Clock(Clock), .Read_Write(Read_Write), .Adress(demultiplexer_1_out2), .Clear(Clear), .IN(IN),
    .OUT(exercicio_03_3_out));
  Exercicio_03 exercicio_03_4 (
    .Clock(Clock), .Read_Write(Read_Write), .Adress(demultiplexer_1_out3), .Clear(Clear), .IN(IN),
    .OUT(exercicio_03_4_out));
  Multiplexer #(.select(2), .width(8), .enable("false")) multiplexer_1 (
    .in0(exercicio_03_1_out), .in1(exercicio_03_2_out), .in2(exercicio_03_3_out), .in3(exercicio_03_4_out),
    .out(OUT), .sel(Adress));

  // Notes on the sheet:
  //   Alvaro Henrique de Araujo Rungue
endmodule
