// Logisim project Circuitos.circ as structural Verilog: 7 circuits, main circuit Guia10_01
// 1x4
module Guia10_01 (
  input  CLK,
  input  [3:0] IN,
  input  R_W,
  input  ADDRESS,
  input  CLR,
  output [3:0] OUT
);

  wire and_1_out, not_1_out, not_2_out, not_3_out, not_4_out;
  wire [3:0] j_k_ff_4_q;

  and and_1 (and_1_out, CLK, R_W, ADDRESS);
  J_K_Flip_Flop j_k_ff_1 (
    .J(IN[3]), .clk(and_1_out), .K(not_1_out), .Q(j_k_ff_4_q[3]), .reset(CLR));  // open: Qn, preset, en
  not not_1 (not_1_out, IN[3]);
  not not_2 (not_2_out, IN[2]);
  J_K_Flip_Flop j_k_ff_2 (
    .J(IN[2]), .clk(and_1_out), .K(not_2_out), .Q(j_k_ff_4_q[2]), .reset(CLR));  // open: Qn, preset, en
  J_K_Flip_Flop j_k_ff_3 (
    .J(IN[1]), .clk(and_1_out), .K(not_3_out), .Q(j_k_ff_4_q[1]), .reset(CLR));  // open: Qn, preset, en
  not not_3 (not_3_out, IN[1]);
  not not_4 (not_4_out, IN[0]);
  J_K_Flip_Flop j_k_ff_4 (
    .J(IN[0]), .clk(and_1_out), .K(not_4_out), .Q(j_k_ff_4_q[0]), .reset(CLR));  // open: Qn, preset, en
  assign OUT = j_k_ff_4_q & {4{ADDRESS}};  // AND_Gate and_2, 4 bits wide

  // Notes on the sheet:
  //   Guia10_01 - Bruno Cezar Andrade Viallet - 396679
endmodule

// 2x4
module Guia10_02 (
  input  CLK,
  input  R_W,
  input  ADRESS,
  input  [3:0] IN,
  input  CLR,
  output [3:0] OUT
);

  wire demultiplexer_1_out0, demultiplexer_1_out1;
  wire [3:0] guia10_01_1_out, guia10_01_2_out;

  Demultiplexer #(.enable("false")) demultiplexer_1 (
    .out0(demultiplexer_1_out0), .out1(demultiplexer_1_out1), .in(1'b1), .sel(ADRESS));
  Guia10_01 guia10_01_1 (
    .CLK(CLK), .R_W(R_W), .ADDRESS(demultiplexer_1_out0), .CLR(CLR), .IN(IN), .OUT(guia10_01_1_out));
  Guia10_01 guia10_01_2 (
    .CLK(CLK), .R_W(R_W), .ADDRESS(demultiplexer_1_out1), .CLR(CLR), .IN(IN), .OUT(guia10_01_2_out));
  Multiplexer #(.width(4), .enable("false")) multiplexer_1 (
    .in0(guia10_01_1_out), .in1(guia10_01_2_out), .out(OUT), .sel(ADRESS));

  // Notes on the sheet:
  //   Guia10_02 - Bruno Cezar Andrade Viallet - 396679
endmodule

// 1x8
module Guia10_03 (
  input  CLK,
  input  R_W,
  input  ADDRESS,
  input  [7:0] IN,
  input  CLR,
  output [7:0] OUT
);

  Guia10_01 guia10_01_1 (.CLK(CLK), .R_W(R_W), .ADDRESS(ADDRESS), .CLR(CLR), .IN(IN[3:0]), .OUT(OUT[3:0]));
  Guia10_01 guia10_01_2 (.CLK(CLK), .R_W(R_W), .ADDRESS(ADDRESS), .CLR(CLR), .IN(IN[7:4]), .OUT(OUT[7:4]));

  // Notes on the sheet:
  //   Guia10_03 - Bruno Cezar Andrade Viallet - 396679
endmodule

module Guia10_04 (
  input  CLK,
  input  R_W,
  input  ADRESS,
  input  [7:0] IN,
  input  CLR,
  output [7:0] OUT
);

  wire demultiplexer_1_out0, demultiplexer_1_out1;
  wire [3:0] guia10_02_1_out, guia10_02_2_out, guia10_02_3_out, guia10_02_4_out;

  Demultiplexer #(.enable("false")) demultiplexer_1 (
    .out0(demultiplexer_1_out0), .out1(demultiplexer_1_out1), .in(1'b1), .sel(ADRESS));
  Guia10_02 guia10_02_1 (
    .CLK(CLK), .R_W(R_W), .ADRESS(demultiplexer_1_out0), .CLR(CLR), .IN(IN[3:0]), .OUT(guia10_02_1_out));
  Guia10_02 guia10_02_2 (
    .CLK(CLK), .R_W(R_W), .ADRESS(demultiplexer_1_out0), .CLR(CLR), .IN(IN[7:4]), .OUT(guia10_02_2_out));
  Guia10_02 guia10_02_3 (
    .CLK(CLK), .R_W(R_W), .ADRESS(demultiplexer_1_out1), .CLR(CLR), .IN(IN[3:0]), .OUT(guia10_02_3_out));
  Guia10_02 guia10_02_4 (
    .CLK(CLK), .R_W(R_W), .ADRESS(demultiplexer_1_out1), .CLR(CLR), .IN(IN[7:4]), .OUT(guia10_02_4_out));
  Multiplexer #(.width(8), .enable("false")) multiplexer_1 (
    .in0({guia10_02_2_out, guia10_02_1_out}), .in1({guia10_02_4_out, guia10_02_3_out}), .out(OUT),
    .sel(ADRESS));

  // Notes on the sheet:
  //   Guia10_04 - Bruno Cezar Andrade Viallet - 396679
endmodule

module Guia10_05 (
  input  CLK,
  input  R_W,
  input  [2:0] ADDRESS,
  input  [7:0] IN,
  input  CLR,
  output [7:0] out_6
);

  wire demultiplexer_1_out0, demultiplexer_1_out1, demultiplexer_1_out2, demultiplexer_1_out3,
       demultiplexer_1_out4, demultiplexer_1_out5, demultiplexer_1_out6, demultiplexer_1_out7;
  wire [7:0] guia10_03_1_out, guia10_03_2_out, guia10_03_3_out, guia10_03_4_out, guia10_03_5_out,
       guia10_03_6_out, guia10_03_7_out, guia10_03_8_out;

  Demultiplexer #(.select(3), .enable("false")) demultiplexer_1 (
    .out0(demultiplexer_1_out0), .out1(demultiplexer_1_out1), .out2(demultiplexer_1_out2),
    .out3(demultiplexer_1_out3), .out4(demultiplexer_1_out4), .out5(demultiplexer_1_out5),
    .out6(demultiplexer_1_out6), .out7(demultiplexer_1_out7), .in(1'b1), .sel(ADDRESS));
  Guia10_03 guia10_03_1 (
    .CLK(CLK), .R_W(R_W), .ADDRESS(demultiplexer_1_out0), .CLR(CLR), .IN(IN), .OUT(guia10_03_1_out));
  Guia10_03 guia10_03_2 (
    .CLK(CLK), .R_W(R_W), .ADDRESS(demultiplexer_1_out1), .CLR(CLR), .IN(IN), .OUT(guia10_03_2_out));
  Guia10_03 guia10_03_3 (
    .CLK(CLK), .R_W(R_W), .ADDRESS(demultiplexer_1_out2), .CLR(CLR), .IN(IN), .OUT(guia10_03_3_out));
  Guia10_03 guia10_03_4 (
    .CLK(CLK), .R_W(R_W), .ADDRESS(demultiplexer_1_out3), .CLR(CLR), .IN(IN), .OUT(guia10_03_4_out));
  Guia10_03 guia10_03_5 (
    .CLK(CLK), .R_W(R_W), .ADDRESS(demultiplexer_1_out4), .CLR(CLR), .IN(IN), .OUT(guia10_03_5_out));
  Guia10_03 guia10_03_6 (
    .CLK(CLK), .R_W(R_W), .ADDRESS(demultiplexer_1_out5), .CLR(CLR), .IN(IN), .OUT(guia10_03_6_out));
  Guia10_03 guia10_03_7 (
    .CLK(CLK), .R_W(R_W), .ADDRESS(demultiplexer_1_out6), .CLR(CLR), .IN(IN), .OUT(guia10_03_7_out));
  Guia10_03 guia10_03_8 (
    .CLK(CLK), .R_W(R_W), .ADDRESS(demultiplexer_1_out7), .CLR(CLR), .IN(IN), .OUT(guia10_03_8_out));
  Multiplexer #(.select(3), .width(8), .enable("false")) multiplexer_1 (
    .in0(guia10_03_1_out), .in1(guia10_03_2_out), .in2(guia10_03_3_out), .in3(guia10_03_4_out),
    .in4(guia10_03_5_out), .in5(guia10_03_6_out), .in6(guia10_03_7_out), .in7(guia10_03_8_out), .out(out_6),
    .sel(ADDRESS));

  // Notes on the sheet:
  //   Guia10_05 - Bruno Cezar Andrade Viallet - 396679
endmodule

module Guia10_06 (
  input  CLK,
  input  R_W,
  input  [15:0] IN,
  input  ADDRESS,
  input  CLR,
  output [15:0] OUT
);

  Guia10_03 guia10_03_1 (.CLK(CLK), .R_W(R_W), .ADDRESS(ADDRESS), .CLR(CLR), .IN(IN[7:0]), .OUT(OUT[7:0]));
  Guia10_03 guia10_03_2 (.CLK(CLK), .R_W(R_W), .ADDRESS(ADDRESS), .CLR(CLR), .IN(IN[15:8]), .OUT(OUT[15:8]));

  // Notes on the sheet:
  //   Guia10_06 - Bruno Cezar Andrade Viallet - 396679
endmodule

module Guia10_07 (
  input  CLK,
  input  R_W,
  input  [1:0] ADDRESS,
  input  [7:0] IN,
  input  CLR,
  output [7:0] OUT
);

  wire demultiplexer_1_out0, demultiplexer_1_out1, demultiplexer_1_out2, demultiplexer_1_out3;
  wire [7:0] guia10_03_1_out, guia10_03_2_out, guia10_03_3_out, guia10_03_4_out;

  Demultiplexer #(.select(2), .enable("false")) demultiplexer_1 (
    .out0(demultiplexer_1_out0), .out1(demultiplexer_1_out1), .out2(demultiplexer_1_out2),
    .out3(demultiplexer_1_out3), .in(1'b1), .sel(ADDRESS));
  Guia10_03 guia10_03_1 (
    .CLK(CLK), .R_W(R_W), .ADDRESS(demultiplexer_1_out0), .CLR(CLR), .IN(IN), .OUT(guia10_03_1_out));
  Guia10_03 guia10_03_2 (
    .CLK(CLK), .R_W(R_W), .ADDRESS(demultiplexer_1_out1), .CLR(CLR), .IN(IN), .OUT(guia10_03_2_out));
  Guia10_03 guia10_03_3 (
    .CLK(CLK), .R_W(R_W), .ADDRESS(demultiplexer_1_out2), .CLR(CLR), .IN(IN), .OUT(guia10_03_3_out));
  Guia10_03 guia10_03_4 (
    .CLK(CLK), .R_W(R_W), .ADDRESS(demultiplexer_1_out3), .CLR(CLR), .IN(IN), .OUT(guia10_03_4_out));
  Multiplexer #(.select(2), .width(8), .enable("false")) multiplexer_1 (
    .in0(guia10_03_1_out), .in1(guia10_03_2_out), .in2(guia10_03_3_out), .in3(guia10_03_4_out), .out(OUT),
    .sel(ADDRESS));

  // Notes on the sheet:
  //   Guia10_07 - Bruno Cezar Andrade Viallet - 396679
endmodule
