// Logisim project circuitos.circ as structural Verilog
// 1X1
module RAM_1X1 (
  input  ADDR,
  input  RW,
  input  CLK,
  input  IN,
  input  CLR,
  output OUT1
);

  wire and_1_out, j_k_ff_1_q, not_1_out;

  and and_1 (and_1_out, ADDR, RW, CLK);
  not not_1 (not_1_out, IN);
  J_K_Flip_Flop j_k_ff_1 (.J(IN), .clk(and_1_out), .K(not_1_out), .Q(j_k_ff_1_q), .reset(CLR));  // open: Qn, preset, en
  and and_2 (OUT1, ADDR, j_k_ff_1_q);
endmodule

// 1X2
module RAM_1X2 (
  input  ADDR,
  input  RW,
  input  CLK,
  input  IN,
  input  IN1,
  input  CLR,
  output OUT0,
  output OUT1
);

  RAM_1X1 ram_1x1_1 (.ADDR(ADDR), .RW(RW), .CLK(CLK), .IN(IN), .CLR(CLR), .OUT1(OUT0));
  RAM_1X1 ram_1x1_2 (.ADDR(ADDR), .RW(RW), .CLK(CLK), .IN(IN1), .CLR(CLR), .OUT1(OUT1));
endmodule

// 1X4
module Exercicio01_RAM_1X4 (
  input  ADDR,
  input  RW,
  input  CLK,
  input  [3:0] in_4,
  input  CLR,
  output [3:0] OUT
);

  RAM_1X2 ram_1x2_1 (
    .ADDR(ADDR), .RW(RW), .CLK(CLK), .IN(in_4[0]), .IN1(in_4[1]), .CLR(CLR), .OUT0(OUT[0]), .OUT1(OUT[1]));
  RAM_1X2 ram_1x2_2 (
    .ADDR(ADDR), .RW(RW), .CLK(CLK), .IN(in_4[2]), .IN1(in_4[3]), .CLR(CLR), .OUT0(OUT[2]), .OUT1(OUT[3]));
endmodule

// 1X8
module Exercicio03_RAM_1X8 (
  input  ADDR,
  input  RW,
  input  CLK,
  input  [7:0] IN,
  input  CLR,
  output [7:0] OUT
);

  Exercicio01_RAM_1X4 exercicio01_ram_1x4_1 (
    .ADDR(ADDR), .RW(RW), .CLK(CLK), .in_4(IN[3:0]), .CLR(CLR), .OUT(OUT[7:4]));
  Exercicio01_RAM_1X4 exercicio01_ram_1x4_2 (
    .ADDR(ADDR), .RW(RW), .CLK(CLK), .in_4(IN[7:4]), .CLR(CLR), .OUT(OUT[3:0]));
endmodule

module Exercicio05_RAM_8X8 (
  input  [2:0] ADDR,
  input  RW,
  input  CLK,
  input  [7:0] in,
  input  CLR,
  input  CLR_2,
  output [7:0] OUT
);

  wire demultiplexer_1_out0, demultiplexer_1_out1, demultiplexer_1_out2, demultiplexer_1_out3,
       demultiplexer_1_out4, demultiplexer_1_out5, demultiplexer_1_out6, demultiplexer_1_out7;
  wire [7:0] exercicio03_ram_1x8_1_out, exercicio03_ram_1x8_2_out, exercicio03_ram_1x8_3_out,
       exercicio03_ram_1x8_4_out, exercicio03_ram_1x8_5_out, exercicio03_ram_1x8_6_out,
       exercicio03_ram_1x8_7_out, exercicio03_ram_1x8_8_out;

  Demultiplexer #(.select(3), .enable("false")) demultiplexer_1 (
    .out0(demultiplexer_1_out0), .out1(demultiplexer_1_out1), .out2(demultiplexer_1_out2),
    .out3(demultiplexer_1_out3), .out4(demultiplexer_1_out4), .out5(demultiplexer_1_out5),
    .out6(demultiplexer_1_out6), .out7(demultiplexer_1_out7), .in(1'b1), .sel(ADDR));
  Exercicio03_RAM_1X8 exercicio03_ram_1x8_1 (
    .ADDR(demultiplexer_1_out0), .RW(RW), .CLK(CLK), .IN(in), .CLR(CLR), .OUT(exercicio03_ram_1x8_1_out));
  Exercicio03_RAM_1X8 exercicio03_ram_1x8_2 (
    .ADDR(demultiplexer_1_out1), .RW(RW), .CLK(CLK), .IN(in), .CLR(CLR), .OUT(exercicio03_ram_1x8_2_out));
  Exercicio03_RAM_1X8 exercicio03_ram_1x8_3 (
    .ADDR(demultiplexer_1_out2), .RW(RW), .CLK(CLK), .IN(in), .CLR(CLR), .OUT(exercicio03_ram_1x8_3_out));
  Exercicio03_RAM_1X8 exercicio03_ram_1x8_4 (
    .ADDR(demultiplexer_1_out3), .RW(RW), .CLK(CLK), .IN(in), .CLR(CLR), .OUT(exercicio03_ram_1x8_4_out));
  Exercicio03_RAM_1X8 exercicio03_ram_1x8_5 (
    .ADDR(demultiplexer_1_out4), .RW(RW), .CLK(CLK), .IN(in), .CLR(CLR), .OUT(exercicio03_ram_1x8_5_out));
  Exercicio03_RAM_1X8 exercicio03_ram_1x8_6 (
    .ADDR(demultiplexer_1_out5), .RW(RW), .CLK(CLK), .IN(in), .CLR(CLR), .OUT(exercicio03_ram_1x8_6_out));
  Exercicio03_RAM_1X8 exercicio03_ram_1x8_7 (
    .ADDR(demultiplexer_1_out6), .RW(RW), .CLK(CLK), .IN(in), .CLR(CLR), .OUT(exercicio03_ram_1x8_7_out));
  Exercicio03_RAM_1X8 exercicio03_ram_1x8_8 (
    .ADDR(demultiplexer_1_out7), .RW(RW), .CLK(CLK), .IN(in), .CLR(CLR), .OUT(exercicio03_ram_1x8_8_out));
  Multiplexer #(.select(3), .width(8), .enable("false")) multiplexer_1 (
    .in0(exercicio03_ram_1x8_1_out), .in1(exercicio03_ram_1x8_2_out), .in2(exercicio03_ram_1x8_3_out),
    .in3(exercicio03_ram_1x8_4_out), .in4(exercicio03_ram_1x8_5_out), .in5(exercicio03_ram_1x8_6_out),
    .in6(exercicio03_ram_1x8_7_out), .in7(exercicio03_ram_1x8_8_out), .out(OUT), .sel(ADDR));
endmodule

// 2X4
module Exercicio02_RAM_2X4 (
  input  ADDR,
  input  RW,
  input  CLK,
  input  [3:0] IN,
  input  in_5,
  output [3:0] OUT
);

  wire demultiplexer_1_out0, demultiplexer_1_out1;
  wire [3:0] exercicio01_ram_1x4_1_out, exercicio01_ram_1x4_2_out;

  Demultiplexer #(.enable("false")) demultiplexer_1 (
    .out0(demultiplexer_1_out0), .out1(demultiplexer_1_out1), .in(1'b1), .sel(ADDR));
  Exercicio01_RAM_1X4 exercicio01_ram_1x4_1 (
    .ADDR(demultiplexer_1_out1), .RW(RW), .CLK(CLK), .in_4(IN), .CLR(in_5), .OUT(exercicio01_ram_1x4_1_out));
  Exercicio01_RAM_1X4 exercicio01_ram_1x4_2 (
    .ADDR(demultiplexer_1_out0), .RW(RW), .CLK(CLK), .in_4(IN), .CLR(in_5), .OUT(exercicio01_ram_1x4_2_out));
  Multiplexer #(.width(4), .disabled(0), .enable("false")) multiplexer_1 (
    .in0(exercicio01_ram_1x4_1_out), .in1(exercicio01_ram_1x4_2_out), .out(OUT), .sel(ADDR));
endmodule

module Exercicio04_RAM_2X8 (
  input  ADDR,
  input  RW,
  input  CLK,
  input  [3:0] IN,
  input  CLR,
  output [3:0] OUT
);

  wire demultiplexer_1_out0, demultiplexer_1_out1;
  wire [3:0] exercicio02_ram_2x4_1_out, exercicio02_ram_2x4_2_out;

  Demultiplexer #(.enable("false")) demultiplexer_1 (
    .out0(demultiplexer_1_out0), .out1(demultiplexer_1_out1), .in(1'b1), .sel(ADDR));
  Exercicio02_RAM_2X4 exercicio02_ram_2x4_1 (
    .ADDR(demultiplexer_1_out0), .RW(RW), .CLK(CLK), .IN(IN), .in_5(CLR), .OUT(exercicio02_ram_2x4_1_out));
  Exercicio02_RAM_2X4 exercicio02_ram_2x4_2 (
    .ADDR(demultiplexer_1_out1), .RW(RW), .CLK(CLK), .IN(IN), .in_5(CLR), .OUT(exercicio02_ram_2x4_2_out));
  Multiplexer #(.width(4), .enable("false")) multiplexer_1 (
    .in0(exercicio02_ram_2x4_2_out), .in1(exercicio02_ram_2x4_1_out), .out(OUT), .sel(ADDR));
endmodule

module EXTRAS01_RAM_1X16 (
  input  ADDR,
  input  RW,
  input  CLK,
  input  [15:0] IN,
  input  CLR,
  output [15:0] OUT
);

  Exercicio01_RAM_1X4 exercicio01_ram_1x4_1 (
    .ADDR(ADDR), .RW(RW), .CLK(CLK), .in_4(IN[3:0]), .CLR(CLR), .OUT(OUT[3:0]));
  Exercicio01_RAM_1X4 exercicio01_ram_1x4_2 (
    .ADDR(ADDR), .RW(RW), .CLK(CLK), .in_4(IN[7:4]), .CLR(CLR), .OUT(OUT[7:4]));
  Exercicio01_RAM_1X4 exercicio01_ram_1x4_3 (
    .ADDR(ADDR), .RW(RW), .CLK(CLK), .in_4(IN[11:8]), .CLR(CLR), .OUT(OUT[11:8]));
  Exercicio01_RAM_1X4 exercicio01_ram_1x4_4 (
    .ADDR(ADDR), .RW(RW), .CLK(CLK), .in_4(IN[15:12]), .CLR(CLR), .OUT(OUT[15:12]));
endmodule

module EXTRAS02_RAM_4X8 (
  input  [1:0] ADDR,
  input  RW,
  input  CLK,
  input  [7:0] IN,
  input  CLR,
  output [7:0] OUT
);

  wire demultiplexer_1_out0, demultiplexer_1_out1, demultiplexer_1_out2, demultiplexer_1_out3;
  wire [7:0] exercicio03_ram_1x8_1_out, exercicio03_ram_1x8_2_out, exercicio03_ram_1x8_3_out,
       exercicio03_ram_1x8_4_out;

  Demultiplexer #(.select(2), .enable("false")) demultiplexer_1 (
    .out0(demultiplexer_1_out0), .out1(demultiplexer_1_out1), .out2(demultiplexer_1_out2),
    .out3(demultiplexer_1_out3), .in(1'b1), .sel(ADDR));
  Exercicio03_RAM_1X8 exercicio03_ram_1x8_1 (
    .ADDR(demultiplexer_1_out0), .RW(RW), .CLK(CLK), .IN(IN), .CLR(CLR), .OUT(exercicio03_ram_1x8_1_out));
  Exercicio03_RAM_1X8 exercicio03_ram_1x8_2 (
    .ADDR(demultiplexer_1_out1), .RW(RW), .CLK(CLK), .IN(IN), .CLR(CLR), .OUT(exercicio03_ram_1x8_2_out));
  Exercicio03_RAM_1X8 exercicio03_ram_1x8_3 (
    .ADDR(demultiplexer_1_out2), .RW(RW), .CLK(CLK), .IN(IN), .OUT(exercicio03_ram_1x8_3_out));  // open: CLR
  Exercicio03_RAM_1X8 exercicio03_ram_1x8_4 (
    .ADDR(demultiplexer_1_out3), .RW(RW), .CLK(CLK), .IN(IN), .OUT(exercicio03_ram_1x8_4_out));  // open: CLR
  Multiplexer #(.select(2), .width(8), .enable("false")) multiplexer_1 (
    .in0(exercicio03_ram_1x8_1_out), .in1(exercicio03_ram_1x8_2_out), .in2(exercicio03_ram_1x8_3_out),
    .in3(exercicio03_ram_1x8_4_out), .out(OUT), .sel(ADDR));
endmodule
