// Logisim project Guia10.circ as structural Verilog
// 1x4
module Memoria_1x4 (
  input  Addr,
  input  R_W,
  input  Clk,
  input  Clr,
  input  [3:0] Entrada,
  output [3:0] Saida
);

  wire and_1_out, j_k_ff_1_q, j_k_ff_2_q, j_k_ff_3_q, j_k_ff_4_q, not_1_out, not_2_out, not_3_out, not_4_out;

  and and_1 (and_1_out, Addr, R_W, Clk);
  and and_2 (Saida[0], Addr, j_k_ff_1_q);
  J_K_Flip_Flop j_k_ff_1 (
    .J(Entrada[0]), .clk(and_1_out), .K(not_1_out), .Q(j_k_ff_1_q), .reset(Clr));  // open: Qn, preset, en
  not not_1 (not_1_out, Entrada[0]);
  and and_3 (Saida[1], Addr, j_k_ff_2_q);
  J_K_Flip_Flop j_k_ff_2 (
    .J(Entrada[1]), .clk(and_1_out), .K(not_2_out), .Q(j_k_ff_2_q), .reset(Clr));  // open: Qn, preset, en
  not not_2 (not_2_out, Entrada[1]);
  and and_4 (Saida[2], Addr, j_k_ff_3_q);
  not not_3 (not_3_out, Entrada[2]);
  J_K_Flip_Flop j_k_ff_3 (
    .J(Entrada[2]), .clk(and_1_out), .K(not_3_out), .Q(j_k_ff_3_q), .reset(Clr));  // open: Qn, preset, en
  not not_4 (not_4_out, Entrada[3]);
  and and_5 (Saida[3], Addr, j_k_ff_4_q);
  J_K_Flip_Flop j_k_ff_4 (
    .J(Entrada[3]), .clk(and_1_out), .K(not_4_out), .Q(j_k_ff_4_q), .reset(Clr));  // open: Qn, preset, en
endmodule

// 2x4
module Memoria_2x4 (
  input  Addr,
  input  R_W,
  input  Clk,
  input  Clr,
  input  [3:0] Entrada,
  output [3:0] Saida
);

  wire demultiplexer_1_out0, demultiplexer_1_out1;
  wire [3:0] memoria_1x4_1_saida, memoria_1x4_2_saida;

  Demultiplexer #(.enable("false")) demultiplexer_1 (
    .out0(demultiplexer_1_out0), .out1(demultiplexer_1_out1), .in(1'b1), .sel(Addr));
  Memoria_1x4 memoria_1x4_1 (
    .Addr(demultiplexer_1_out0), .R_W(R_W), .Entrada(Entrada), .Clr(Clr), .Saida(memoria_1x4_1_saida),
    .Clk(Clk));
  Memoria_1x4 memoria_1x4_2 (
    .Addr(demultiplexer_1_out1), .R_W(R_W), .Entrada(Entrada), .Clr(Clr), .Saida(memoria_1x4_2_saida),
    .Clk(Clk));
  Multiplexer #(.width(4), .enable("false")) multiplexer_1 (
    .in0(memoria_1x4_1_saida), .in1(memoria_1x4_2_saida), .out(Saida), .sel(Addr));
endmodule

// 1x8
module Memoria_1x8 (
  input  Addr,
  input  R_W,
  input  Clk,
  input  Clr,
  input  [7:0] Entrada,
  output [7:0] Output
);

  Memoria_1x4 memoria_1x4_1 (.Addr(Addr), .R_W(R_W), .Entrada(Entrada[3:0]), .Clr(Clr), .Saida(Output[3:0]), .Clk(Clk));
  Memoria_1x4 memoria_1x4_2 (.Addr(Addr), .R_W(R_W), .Entrada(Entrada[7:4]), .Clr(Clr), .Saida(Output[7:4]), .Clk(Clk));
endmodule

// 2x8
module Memoria_2x8 (
  input  Addr,
  input  R_W,
  input  Clk,
  input  Clr,
  input  [7:0] Entrada,
  output [7:0] Saida
);

  wire demultiplexer_1_out0, demultiplexer_1_out1;
  wire [3:0] memoria_2x4_1_saida, memoria_2x4_2_saida, memoria_2x4_3_saida, memoria_2x4_4_saida;

  Demultiplexer demultiplexer_1 (
    .out0(demultiplexer_1_out0), .out1(demultiplexer_1_out1), .in(1'b1), .sel(Addr));  // open: en
  Memoria_2x4 memoria_2x4_1 (
    .Addr(demultiplexer_1_out0), .R_W(R_W), .Clk(Clk), .Clr(Clr), .Entrada(Entrada[3:0]),
    .Saida(memoria_2x4_1_saida));
  Memoria_2x4 memoria_2x4_2 (
    .Addr(demultiplexer_1_out0), .R_W(R_W), .Clk(Clk), .Clr(Clr), .Entrada(Entrada[7:4]),
    .Saida(memoria_2x4_2_saida));
  Memoria_2x4 memoria_2x4_3 (
    .Addr(demultiplexer_1_out1), .R_W(R_W), .Clk(Clk), .Clr(Clr), .Entrada(Entrada[3:0]),
    .Saida(memoria_2x4_3_saida));
  Memoria_2x4 memoria_2x4_4 (
    .Addr(demultiplexer_1_out1), .R_W(R_W), .Clk(Clk), .Clr(Clr), .Entrada(Entrada[7:4]),
    .Saida(memoria_2x4_4_saida));
  Multiplexer #(.width(8)) multiplexer_1 (
    .in0({memoria_2x4_2_saida, memoria_2x4_1_saida}), .in1({memoria_2x4_4_saida, memoria_2x4_3_saida}),
    .out(Saida), .sel(Addr));  // open: en
endmodule

// 8x8
module Memoria_8x8 (
  input  [2:0] Addr,
  input  R_W,
  input  Clk,
  input  Clr,
  input  [7:0] Entrada,
  output [7:0] Saida
);

  wire demultiplexer_1_out0, demultiplexer_1_out1, demultiplexer_1_out2, demultiplexer_1_out3,
       demultiplexer_1_out4, demultiplexer_1_out5, demultiplexer_1_out6, demultiplexer_1_out7;
  wire [7:0] memoria_1x8_1_output, memoria_1x8_2_output, memoria_1x8_3_output, memoria_1x8_4_output,
       memoria_1x8_5_output, memoria_1x8_6_output, memoria_1x8_7_output, memoria_1x8_8_output;

  Demultiplexer #(.select(3), .enable("false")) demultiplexer_1 (
    .out0(demultiplexer_1_out0), .out1(demultiplexer_1_out1), .out2(demultiplexer_1_out2),
    .out3(demultiplexer_1_out3), .out4(demultiplexer_1_out4), .out5(demultiplexer_1_out5),
    .out6(demultiplexer_1_out6), .out7(demultiplexer_1_out7), .in(1'b1), .sel(Addr));
  Memoria_1x8 memoria_1x8_1 (
    .Addr(demultiplexer_1_out0), .R_W(R_W), .Clk(Clk), .Clr(Clr), .Entrada(Entrada),
    .Output(memoria_1x8_1_output));
  Memoria_1x8 memoria_1x8_2 (
    .Addr(demultiplexer_1_out1), .R_W(R_W), .Clk(Clk), .Clr(Clr), .Entrada(Entrada),
    .Output(memoria_1x8_2_output));
  Memoria_1x8 memoria_1x8_3 (
    .Addr(demultiplexer_1_out2), .R_W(R_W), .Clk(Clk), .Clr(Clr), .Entrada(Entrada),
    .Output(memoria_1x8_3_output));
  Memoria_1x8 memoria_1x8_4 (
    .Addr(demultiplexer_1_out3), .R_W(R_W), .Clk(Clk), .Clr(Clr), .Entrada(Entrada),
    .Output(memoria_1x8_4_output));
  Memoria_1x8 memoria_1x8_5 (
    .Addr(demultiplexer_1_out4), .R_W(R_W), .Clk(Clk), .Clr(Clr), .Entrada(Entrada),
    .Output(memoria_1x8_5_output));
  Memoria_1x8 memoria_1x8_6 (
    .Addr(demultiplexer_1_out5), .R_W(R_W), .Clk(Clk), .Clr(Clr), .Entrada(Entrada),
    .Output(memoria_1x8_6_output));
  Memoria_1x8 memoria_1x8_7 (
    .Addr(demultiplexer_1_out6), .R_W(R_W), .Clk(Clk), .Clr(Clr), .Entrada(Entrada),
    .Output(memoria_1x8_7_output));
  Memoria_1x8 memoria_1x8_8 (
    .Addr(demultiplexer_1_out7), .R_W(R_W), .Clk(Clk), .Clr(Clr), .Entrada(Entrada),
    .Output(memoria_1x8_8_output));
  Multiplexer #(.select(3), .width(8), .enable("false")) multiplexer_1 (
    .in0(memoria_1x8_1_output), .in1(memoria_1x8_2_output), .in2(memoria_1x8_3_output),
    .in3(memoria_1x8_4_output), .in4(memoria_1x8_5_output), .in5(memoria_1x8_6_output),
    .in6(memoria_1x8_7_output), .in7(memoria_1x8_8_output), .out(Saida), .sel(Addr));
endmodule

// 1x16
module Memoria_1x16 (
  input  Addr,
  input  R_W,
  input  Clk,
  input  Clr,
  input  [15:0] Entrada,
  output [15:0] Output
);

  Memoria_1x8 memoria_1x8_1 (
    .Addr(Addr), .R_W(R_W), .Clk(Clk), .Clr(Clr), .Entrada(Entrada[7:0]), .Output(Output[7:0]));
  Memoria_1x8 memoria_1x8_2 (
    .Addr(Addr), .R_W(R_W), .Clk(Clk), .Clr(Clr), .Entrada(Entrada[15:8]), .Output(Output[15:8]));
endmodule

// 4x8
module Memoria_4x8 (
  input  [1:0] Addr,
  input  R_W,
  input  Clk,
  input  Clr,
  input  [7:0] Entrada,
  output [7:0] Saida
);

  wire demultiplexer_1_out0, demultiplexer_1_out1, demultiplexer_1_out2, demultiplexer_1_out3;
  wire [7:0] memoria_1x8_1_output, memoria_1x8_2_output, memoria_1x8_3_output, memoria_1x8_4_output;

  Demultiplexer #(.select(2), .enable("false")) demultiplexer_1 (
    .out0(demultiplexer_1_out0), .out1(demultiplexer_1_out1), .out2(demultiplexer_1_out2),
    .out3(demultiplexer_1_out3), .in(1'b1), .sel(Addr));
  Memoria_1x8 memoria_1x8_1 (
    .Addr(demultiplexer_1_out0), .R_W(R_W), .Clk(Clk), .Clr(Clr), .Entrada(Entrada),
    .Output(memoria_1x8_1_output));
  Memoria_1x8 memoria_1x8_2 (
    .Addr(demultiplexer_1_out1), .R_W(R_W), .Clk(Clk), .Clr(Clr), .Entrada(Entrada),
    .Output(memoria_1x8_2_output));
  Memoria_1x8 memoria_1x8_3 (
    .Addr(demultiplexer_1_out2), .R_W(R_W), .Clk(Clk), .Clr(Clr), .Entrada(Entrada),
    .Output(memoria_1x8_3_output));
  Memoria_1x8 memoria_1x8_4 (
    .Addr(demultiplexer_1_out3), .R_W(R_W), .Clk(Clk), .Clr(Clr), .Entrada(Entrada),
    .Output(memoria_1x8_4_output));
  Multiplexer #(.select(2), .width(8), .enable("false")) multiplexer_1 (
    .in0(memoria_1x8_1_output), .in1(memoria_1x8_2_output), .in2(memoria_1x8_3_output),
    .in3(memoria_1x8_4_output), .out(Saida), .sel(Addr));
endmodule
