// Logisim project mux.circ as structural Verilog: 1 circuit, main circuit main
module main (
  input  in_1,
  input  in_2,
  input  in_3,
  input  in_4,
  input  in_5,
  input  in_6,
  input  in_7,
  output out_8,
  output out_9,
  output out_10,
  output out_11,
  output out_12,
  output out_13
);

  wire and_1_out, and_2_out, not_1_out, not_2_out;

  Demultiplexer #(.enable("false")) demultiplexer_1 (.out0(out_10), .out1(out_11), .in(1'b1), .sel(in_6));
  Multiplexer #(.enable("false")) multiplexer_1 (.in0(in_2), .in1(in_3), .out(out_8), .sel(in_6));
  and and_1 (and_1_out, in_1, not_1_out);
  not not_1 (not_1_out, in_5);
  and and_2 (and_2_out, in_4, in_5);
  not not_2 (not_2_out, in_7);
  and and_3 (out_12, not_2_out, 1'b1);
  and and_4 (out_13, in_7, 1'b1);
  or or_1 (out_9, and_1_out, and_2_out);
endmodule
