// Logisim project Circuito Guia10.circ as structural Verilog
module _1X1 (
  input  Addr,
  input  R_W,
  input  CLK,
  input  IN,
  input  CLR,
  output OUT
);

  wire and_1_out, d_ff_1_q;

  and and_1 (and_1_out, Addr, R_W, CLK);
  D_Flip_Flop d_ff_1 (.clk(and_1_out), .D(IN), .Q(d_ff_1_q), .reset(CLR));  // open: Qn, preset, en
  and and_2 (OUT, Addr, d_ff_1_q);
endmodule

module _1X2 (
  input  Addr,
  input  R_W,
  input  CLK,
  input  IN0,
  input  IN1,
  input  CLR,
  output OUT0,
  output OUT1
);

  _1X1 u_1x1_1 (.Addr(Addr), .R_W(R_W), .CLK(CLK), .IN(IN0), .CLR(CLR), .OUT(OUT0));
  _1X1 u_1x1_2 (.Addr(Addr), .R_W(R_W), .CLK(CLK), .IN(IN1), .CLR(CLR), .OUT(OUT1));
endmodule

module _1X4 (
  input  Addr,
  input  R_W,
  input  CLK,
  input  IN0,
  input  IN1,
  input  IN2,
  input  IN3,
  input  CLR,
  output OUT0,
  output OUT1,
  output OUT2,
  output OUT3
);

  _1X2 u_1x2_1 (.Addr(Addr), .R_W(R_W), .CLK(CLK), .IN0(IN0), .IN1(IN1), .CLR(CLR), .OUT0(OUT0), .OUT1(OUT1));
  _1X2 u_1x2_2 (.Addr(Addr), .R_W(R_W), .CLK(CLK), .IN0(IN2), .IN1(IN3), .CLR(CLR), .OUT0(OUT2), .OUT1(OUT3));
endmodule

// 2x4
module _2X4 (
  input  Addr,
  input  R_W,
  input  CLK,
  input  IN0,
  input  IN1,
  input  IN2,
  input  IN3,
  input  in_8,
  output [3:0] OUT0
);

  wire demultiplexer_1_out0, demultiplexer_1_out1;
  wire [3:0] n1x4_1_out0, n1x4_2_out0;

  Demultiplexer #(.enable("false")) demultiplexer_1 (
    .out0(demultiplexer_1_out0), .out1(demultiplexer_1_out1), .in(1'b1), .sel(Addr));
  _1X4 u_1x4_1 (
    .Addr(demultiplexer_1_out0), .R_W(R_W), .CLK(CLK), .IN0(IN0), .IN1(IN1), .IN2(IN2), .IN3(IN3),
    .CLR(in_8), .OUT0(n1x4_1_out0[0]), .OUT1(n1x4_1_out0[1]), .OUT2(n1x4_1_out0[2]), .OUT3(n1x4_1_out0[3]));
  _1X4 u_1x4_2 (
    .Addr(demultiplexer_1_out1), .R_W(R_W), .CLK(CLK), .IN0(IN0), .IN1(IN1), .IN2(IN2), .IN3(IN3),
    .CLR(in_8), .OUT0(n1x4_2_out0[0]), .OUT1(n1x4_2_out0[1]), .OUT2(n1x4_2_out0[2]), .OUT3(n1x4_2_out0[3]));
  Multiplexer #(.width(4), .enable("false")) multiplexer_1 (
    .in0(n1x4_1_out0), .in1(n1x4_2_out0), .out(OUT0), .sel(Addr));
endmodule

// 1x8
module _1X8 (
  input  Addr,
  input  R_W,
  input  CLK,
  input  [7:0] IN,
  input  in_5,
  output [7:0] out_6
);

  _1X4 u_1x4_1 (
    .Addr(Addr), .R_W(R_W), .CLK(CLK), .IN0(IN[0]), .IN1(IN[1]), .IN2(IN[2]), .IN3(IN[3]), .CLR(in_5),
    .OUT0(out_6[0]), .OUT1(out_6[1]), .OUT2(out_6[2]), .OUT3(out_6[3]));
  _1X4 u_1x4_2 (
    .Addr(Addr), .R_W(R_W), .CLK(CLK), .IN0(IN[4]), .IN1(IN[5]), .IN2(IN[6]), .IN3(IN[7]), .CLR(in_5),
    .OUT0(out_6[4]), .OUT1(out_6[5]), .OUT2(out_6[6]), .OUT3(out_6[7]));
endmodule

module _2X8 (
  input  Addr,
  input  R_W,
  input  CLK,
  input  [7:0] IN,
  output [7:0] OUT
);

  _2X4 u_2x4_1 (
    .Addr(Addr), .R_W(R_W), .CLK(CLK), .IN0(IN[0]), .IN1(IN[1]), .IN2(IN[2]), .IN3(IN[3]), .OUT0(OUT[3:0]));  // open: in_8
  _2X4 u_2x4_2 (
    .Addr(Addr), .R_W(R_W), .CLK(CLK), .IN0(IN[4]), .IN1(IN[5]), .IN2(IN[6]), .IN3(IN[7]), .OUT0(OUT[7:4]));  // open: in_8
endmodule

module _8x8 (
  input  [2:0] Addr,
  input  R_W,
  input  CLK,
  input  [7:0] IN,
  input  CLR,
  output [7:0] OUT
);

  wire demultiplexer_1_out0, demultiplexer_1_out1, demultiplexer_1_out2, demultiplexer_1_out3,
       demultiplexer_1_out4, demultiplexer_1_out5, demultiplexer_1_out6, demultiplexer_1_out7;
  wire [7:0] n1x8_1_out_6, n1x8_2_out_6, n1x8_3_out_6, n1x8_4_out_6, n1x8_5_out_6, n1x8_6_out_6,
       n1x8_7_out_6, n1x8_8_out_6;

  Demultiplexer #(.select(3), .enable("false")) demultiplexer_1 (
    .out0(demultiplexer_1_out0), .out1(demultiplexer_1_out1), .out2(demultiplexer_1_out2),
    .out3(demultiplexer_1_out3), .out4(demultiplexer_1_out4), .out5(demultiplexer_1_out5),
    .out6(demultiplexer_1_out6), .out7(demultiplexer_1_out7), .in(1'b1), .sel(Addr));
  _1X8 u_1x8_1 (.Addr(demultiplexer_1_out0), .R_W(R_W), .CLK(CLK), .IN(IN), .in_5(CLR), .out_6(n1x8_1_out_6));
  _1X8 u_1x8_2 (.Addr(demultiplexer_1_out1), .R_W(R_W), .CLK(CLK), .IN(IN), .in_5(CLR), .out_6(n1x8_2_out_6));
  _1X8 u_1x8_3 (.Addr(demultiplexer_1_out2), .R_W(R_W), .CLK(CLK), .IN(IN), .in_5(CLR), .out_6(n1x8_3_out_6));
  _1X8 u_1x8_4 (.Addr(demultiplexer_1_out3), .R_W(R_W), .CLK(CLK), .IN(IN), .in_5(CLR), .out_6(n1x8_4_out_6));
  _1X8 u_1x8_5 (.Addr(demultiplexer_1_out4), .R_W(R_W), .CLK(CLK), .IN(IN), .in_5(CLR), .out_6(n1x8_5_out_6));
  _1X8 u_1x8_6 (.Addr(demultiplexer_1_out5), .R_W(R_W), .CLK(CLK), .IN(IN), .in_5(CLR), .out_6(n1x8_6_out_6));
  _1X8 u_1x8_7 (.Addr(demultiplexer_1_out6), .R_W(R_W), .CLK(CLK), .IN(IN), .in_5(CLR), .out_6(n1x8_7_out_6));
  _1X8 u_1x8_8 (.Addr(demultiplexer_1_out7), .R_W(R_W), .CLK(CLK), .IN(IN), .in_5(CLR), .out_6(n1x8_8_out_6));
  Multiplexer #(.select(3), .width(8), .enable("false")) multiplexer_1 (
    .in0(n1x8_1_out_6), .in1(n1x8_2_out_6), .in2(n1x8_3_out_6), .in3(n1x8_4_out_6), .in4(n1x8_5_out_6),
    .in5(n1x8_6_out_6), .in6(n1x8_7_out_6), .in7(n1x8_8_out_6), .out(OUT), .sel(Addr));
endmodule

module _1x16 (
  input  Addr,
  input  R_W,
  input  CLK,
  input  [15:0] IN0,
  input  CLR,
  output [15:0] OUT
);

  _1X8 u_1x8_1 (.Addr(Addr), .R_W(R_W), .CLK(CLK), .IN(IN0[7:0]), .in_5(CLR), .out_6(OUT[7:0]));
  _1X8 u_1x8_2 (.Addr(Addr), .R_W(R_W), .CLK(CLK), .IN(IN0[15:8]), .in_5(CLR), .out_6(OUT[15:8]));
endmodule

module _4x8 (
  input  [1:0] Addr,
  input  R_W,
  input  CLK,
  input  [7:0] IN0,
  input  in_5,
  output [7:0] OUT
);

  wire demultiplexer_1_out0, demultiplexer_1_out1, demultiplexer_1_out2, demultiplexer_1_out3;
  wire [7:0] n1x8_1_out_6, n1x8_2_out_6, n1x8_3_out_6, n1x8_4_out_6;

  Demultiplexer #(.select(2), .enable("false")) demultiplexer_1 (
    .out0(demultiplexer_1_out0), .out1(demultiplexer_1_out1), .out2(demultiplexer_1_out2),
    .out3(demultiplexer_1_out3), .in(1'b1), .sel(Addr));
  _1X8 u_1x8_1 (.Addr(demultiplexer_1_out0), .R_W(R_W), .CLK(CLK), .IN(IN0), .in_5(in_5), .out_6(n1x8_1_out_6));
  _1X8 u_1x8_2 (.Addr(demultiplexer_1_out1), .R_W(R_W), .CLK(CLK), .IN(IN0), .in_5(in_5), .out_6(n1x8_2_out_6));
  _1X8 u_1x8_3 (.Addr(demultiplexer_1_out2), .R_W(R_W), .CLK(CLK), .IN(IN0), .in_5(in_5), .out_6(n1x8_3_out_6));
  _1X8 u_1x8_4 (.Addr(demultiplexer_1_out3), .R_W(R_W), .CLK(CLK), .IN(IN0), .in_5(in_5), .out_6(n1x8_4_out_6));
  Multiplexer #(.select(2), .width(8), .enable("false")) multiplexer_1 (
    .in0(n1x8_1_out_6), .in1(n1x8_2_out_6), .in2(n1x8_3_out_6), .in3(n1x8_4_out_6), .out(OUT), .sel(Addr));
endmodule
