// Logisim project Circuitos.circ as structural Verilog: 7 circuits, main circuit RAM 1x4
// 1x4
module RAM_1x4 (
  input  Addr,
  input  R_W,
  input  Clk,
  input  [3:0] In,
  input  Clr,
  output [3:0] Output
);

  wire and_1_out, j_k_ff_1_q, j_k_ff_2_q, j_k_ff_3_q, j_k_ff_4_q, not_1_out, not_2_out, not_3_out, not_4_out;

  and and_1 (and_1_out, Addr, R_W, Clk);
  not not_1 (not_1_out, In[0]);
  and and_2 (Output[0], Addr, j_k_ff_1_q);
  J_K_Flip_Flop j_k_ff_1 (
    .J(In[0]), .clk(and_1_out), .K(not_1_out), .Q(j_k_ff_1_q), .reset(Clr));  // open: Qn, preset, en
  not not_2 (not_2_out, In[1]);
  and and_3 (Output[1], Addr, j_k_ff_2_q);
  J_K_Flip_Flop j_k_ff_2 (
    .J(In[1]), .clk(and_1_out), .K(not_2_out), .Q(j_k_ff_2_q), .reset(Clr));  // open: Qn, preset, en
  not not_3 (not_3_out, In[2]);
  and and_4 (Output[2], Addr, j_k_ff_3_q);
  J_K_Flip_Flop j_k_ff_3 (
    .J(In[2]), .clk(and_1_out), .K(not_3_out), .Q(j_k_ff_3_q), .reset(Clr));  // open: Qn, preset, en
  and and_5 (Output[3], Addr, j_k_ff_4_q);
  J_K_Flip_Flop j_k_ff_4 (
    .J(In[3]), .clk(and_1_out), .K(not_4_out), .Q(j_k_ff_4_q), .reset(Clr));  // open: Qn, preset, en
  not not_4 (not_4_out, In[3]);
endmodule

// 2x4
module RAM_2x4 (
  input  Addr,
  input  R_W,
  input  CLK,
  input  [3:0] In,
  input  Clr,
  output [3:0] out_6
);

  wire demultiplexer_1_out0, demultiplexer_1_out1;
  wire [3:0] ram_1x4_1_output, ram_1x4_2_output;

  Demultiplexer #(.enable("false")) demultiplexer_1 (
    .out0(demultiplexer_1_out0), .out1(demultiplexer_1_out1), .in(1'b1), .sel(Addr));
  RAM_1x4 ram_1x4_1 (.Addr(demultiplexer_1_out0), .R_W(R_W), .Clk(CLK), .In(In), .Clr(Clr), .Output(ram_1x4_1_output));
  RAM_1x4 ram_1x4_2 (.Addr(demultiplexer_1_out1), .R_W(R_W), .Clk(CLK), .In(In), .Clr(Clr), .Output(ram_1x4_2_output));
  Multiplexer #(.width(4), .enable("false")) multiplexer_1 (
    .in0(ram_1x4_1_output), .in1(ram_1x4_2_output), .out(out_6), .sel(Addr));
endmodule

// 1x8
module RAM_1x8 (
  input  Addr,
  input  R_W,
  input  Clk,
  input  Clr,
  input  [7:0] In,
  output [7:0] Out
);

  RAM_1x4 ram_1x4_1 (.Addr(Addr), .R_W(R_W), .Clk(Clk), .In(In[3:0]), .Clr(Clr), .Output(Out[3:0]));
  RAM_1x4 ram_1x4_2 (.Addr(Addr), .R_W(R_W), .Clk(Clk), .In(In[7:4]), .Clr(Clr), .Output(Out[7:4]));
endmodule

module RAM_2x8 (
  input  Addr,
  input  R_W,
  input  CLK,
  input  CLR,
  input  [7:0] InPut,
  output [7:0] Out
);

  wire demultiplexer_1_out0, demultiplexer_1_out1;
  wire [3:0] ram_2x4_1_out_6, ram_2x4_2_out_6, ram_2x4_3_out_6, ram_2x4_4_out_6;

  Demultiplexer #(.enable("false")) demultiplexer_1 (
    .out0(demultiplexer_1_out0), .out1(demultiplexer_1_out1), .in(1'b1), .sel(Addr));
  RAM_2x4 ram_2x4_1 (
    .Addr(demultiplexer_1_out0), .R_W(R_W), .CLK(CLK), .In(InPut[3:0]), .Clr(CLR), .out_6(ram_2x4_1_out_6));
  RAM_2x4 ram_2x4_2 (
    .Addr(demultiplexer_1_out0), .R_W(R_W), .CLK(CLK), .In(InPut[7:4]), .Clr(CLR), .out_6(ram_2x4_2_out_6));
  RAM_2x4 ram_2x4_3 (
    .Addr(demultiplexer_1_out1), .R_W(R_W), .CLK(CLK), .In(InPut[3:0]), .Clr(CLR), .out_6(ram_2x4_3_out_6));
  RAM_2x4 ram_2x4_4 (
    .Addr(demultiplexer_1_out1), .R_W(R_W), .CLK(CLK), .In(InPut[7:4]), .Clr(CLR), .out_6(ram_2x4_4_out_6));
  Multiplexer #(.width(8), .enable("false")) multiplexer_1 (
    .in0({ram_2x4_2_out_6, ram_2x4_1_out_6}), .in1({ram_2x4_4_out_6, ram_2x4_3_out_6}), .out(Out), .sel(Addr));
endmodule

module RAM_8x8 (
  input  [2:0] Addr,
  input  R_W,
  input  CLK,
  input  CLR,
  input  [7:0] InPut,
  output [7:0] out_6
);

  wire demultiplexer_1_out0, demultiplexer_1_out1, demultiplexer_1_out2, demultiplexer_1_out3,
       demultiplexer_1_out4, demultiplexer_1_out5, demultiplexer_1_out6, demultiplexer_1_out7;
  wire [7:0] ram_1x8_1_out, ram_1x8_2_out, ram_1x8_3_out, ram_1x8_4_out, ram_1x8_5_out, ram_1x8_6_out,
       ram_1x8_7_out, ram_1x8_8_out;

  Demultiplexer #(.select(3), .enable("false")) demultiplexer_1 (
    .out0(demultiplexer_1_out0), .out1(demultiplexer_1_out1), .out2(demultiplexer_1_out2),
    .out3(demultiplexer_1_out3), .out4(demultiplexer_1_out4), .out5(demultiplexer_1_out5),
    .out6(demultiplexer_1_out6), .out7(demultiplexer_1_out7), .in(1'b1), .sel(Addr));
  RAM_1x8 ram_1x8_1 (.Addr(demultiplexer_1_out0), .R_W(R_W), .Clk(CLK), .Clr(CLR), .In(InPut), .Out(ram_1x8_1_out));
  RAM_1x8 ram_1x8_2 (.Addr(demultiplexer_1_out1), .R_W(R_W), .Clk(CLK), .Clr(CLR), .In(InPut), .Out(ram_1x8_2_out));
  RAM_1x8 ram_1x8_3 (.Addr(demultiplexer_1_out2), .R_W(R_W), .Clk(CLK), .Clr(CLR), .In(InPut), .Out(ram_1x8_3_out));
  RAM_1x8 ram_1x8_4 (.Addr(demultiplexer_1_out3), .R_W(R_W), .Clk(CLK), .Clr(CLR), .In(InPut), .Out(ram_1x8_4_out));
  RAM_1x8 ram_1x8_5 (.Addr(demultiplexer_1_out4), .R_W(R_W), .Clk(CLK), .Clr(CLR), .In(InPut), .Out(ram_1x8_5_out));
  RAM_1x8 ram_1x8_6 (.Addr(demultiplexer_1_out5), .R_W(R_W), .Clk(CLK), .Clr(CLR), .In(InPut), .Out(ram_1x8_6_out));
  RAM_1x8 ram_1x8_7 (.Addr(demultiplexer_1_out6), .R_W(R_W), .Clk(CLK), .Clr(CLR), .In(InPut), .Out(ram_1x8_7_out));
  RAM_1x8 ram_1x8_8 (.Addr(demultiplexer_1_out7), .R_W(R_W), .Clk(CLK), .Clr(CLR), .In(InPut), .Out(ram_1x8_8_out));
  Multiplexer #(.select(3), .width(8), .enable("false")) multiplexer_1 (
    .in0(ram_1x8_1_out), .in1(ram_1x8_2_out), .in2(ram_1x8_3_out), .in3(ram_1x8_4_out), .in4(ram_1x8_5_out),
    .in5(ram_1x8_6_out), .in6(ram_1x8_7_out), .in7(ram_1x8_8_out), .out(out_6), .sel(Addr));
endmodule

module RAM_1x16 (
  input  Addr,
  input  R_W,
  input  CLK,
  input  CLR,
  input  [15:0] InPut,
  output [15:0] out_6
);

  RAM_1x8 ram_1x8_1 (.Addr(Addr), .R_W(R_W), .Clk(CLK), .Clr(CLR), .In(InPut[7:0]), .Out(out_6[7:0]));
  RAM_1x8 ram_1x8_2 (.Addr(Addr), .R_W(R_W), .Clk(CLK), .Clr(CLR), .In(InPut[15:8]), .Out(out_6[15:8]));
endmodule

module RAM_4x8 (
  input  [1:0] Addr,
  input  R_W,
  input  CLK,
  input  CLR,
  input  [7:0] InPut,
  output [7:0] out_6
);

  wire demultiplexer_1_out0, demultiplexer_1_out1, demultiplexer_1_out2, demultiplexer_1_out3;
  wire [7:0] ram_1x8_1_out, ram_1x8_2_out, ram_1x8_3_out, ram_1x8_4_out;

  Demultiplexer #(.select(2), .enable("false")) demultiplexer_1 (
    .out0(demultiplexer_1_out0), .out1(demultiplexer_1_out1), .out2(demultiplexer_1_out2),
    .out3(demultiplexer_1_out3), .in(1'b1), .sel(Addr));
  RAM_1x8 ram_1x8_1 (.Addr(demultiplexer_1_out0), .R_W(R_W), .Clk(CLK), .Clr(CLR), .In(InPut), .Out(ram_1x8_1_out));
  RAM_1x8 ram_1x8_2 (.Addr(demultiplexer_1_out1), .R_W(R_W), .Clk(CLK), .Clr(CLR), .In(InPut), .Out(ram_1x8_2_out));
  RAM_1x8 ram_1x8_3 (.Addr(demultiplexer_1_out2), .R_W(R_W), .Clk(CLK), .Clr(CLR), .In(InPut), .Out(ram_1x8_3_out));
  RAM_1x8 ram_1x8_4 (.Addr(demultiplexer_1_out3), .R_W(R_W), .Clk(CLK), .Clr(CLR), .In(InPut), .Out(ram_1x8_4_out));
  Multiplexer #(.select(2), .width(8), .enable("false")) multiplexer_1 (
    .in0(ram_1x8_1_out), .in1(ram_1x8_2_out), .in2(ram_1x8_3_out), .in3(ram_1x8_4_out), .out(out_6),
    .sel(Addr));
endmodule
