// Logisim project Guia_10.circ as structural Verilog: 7 circuits, main circuit Exercicio101
// 1x4
module Exercicio101 (
  input  Addr,
  input  R_W,
  input  Clk,
  input  [3:0] In,
  input  Clr,
  output [3:0] Out
);

  wire and_1_out, j_k_ff_1_q, j_k_ff_2_q, j_k_ff_3_q, j_k_ff_4_q, not_1_out, not_2_out, not_3_out, not_4_out;

  and and_1 (and_1_out, Addr, R_W, Clk);
  not not_1 (not_1_out, In[0]);
  and and_2 (Out[0], Addr, j_k_ff_1_q);
  J_K_Flip_Flop j_k_ff_1 (
    .J(In[0]), .clk(and_1_out), .K(not_1_out), .Q(j_k_ff_1_q), .reset(Clr));  // open: Qn, preset, en
  not not_2 (not_2_out, In[1]);
  and and_3 (Out[1], Addr, j_k_ff_2_q);
  J_K_Flip_Flop j_k_ff_2 (
    .J(In[1]), .clk(and_1_out), .K(not_2_out), .Q(j_k_ff_2_q), .reset(Clr));  // open: Qn, preset, en
  not not_3 (not_3_out, In[2]);
  and and_4 (Out[2], Addr, j_k_ff_3_q);
  J_K_Flip_Flop j_k_ff_3 (
    .J(In[2]), .clk(and_1_out), .K(not_3_out), .Q(j_k_ff_3_q), .reset(Clr));  // open: Qn, preset, en
  and and_5 (Out[3], Addr, j_k_ff_4_q);
  J_K_Flip_Flop j_k_ff_4 (
    .J(In[3]), .clk(and_1_out), .K(not_4_out), .Q(j_k_ff_4_q), .reset(Clr));  // open: Qn, preset, en
  not not_4 (not_4_out, In[3]);
endmodule

// 2x4
module Exercicio102 (
  input  Addr,
  input  R_W,
  input  CLK,
  input  [3:0] In,
  input  Clr,
  output [3:0] Out
);

  wire demultiplexer_1_out0, demultiplexer_1_out1;
  wire [3:0] exercicio101_1_out, exercicio101_2_out;

  Demultiplexer #(.enable("false")) demultiplexer_1 (
    .out0(demultiplexer_1_out0), .out1(demultiplexer_1_out1), .in(1'b1), .sel(Addr));
  Exercicio101 exercicio101_1 (
    .Addr(demultiplexer_1_out0), .R_W(R_W), .Clk(CLK), .In(In), .Clr(Clr), .Out(exercicio101_1_out));
  Exercicio101 exercicio101_2 (
    .Addr(demultiplexer_1_out1), .R_W(R_W), .Clk(CLK), .In(In), .Clr(Clr), .Out(exercicio101_2_out));
  Multiplexer #(.width(4), .enable("false")) multiplexer_1 (
    .in0(exercicio101_1_out), .in1(exercicio101_2_out), .out(Out), .sel(Addr));
endmodule

// 1x8
module Exercicio103 (
  input  Addr,
  input  R_W,
  input  Clk,
  input  Clr,
  input  [7:0] In,
  output [7:0] Out
);

  Exercicio101 exercicio101_1 (.Addr(Addr), .R_W(R_W), .Clk(Clk), .In(In[3:0]), .Clr(Clr), .Out(Out[3:0]));
  Exercicio101 exercicio101_2 (.Addr(Addr), .R_W(R_W), .Clk(Clk), .In(In[7:4]), .Clr(Clr), .Out(Out[7:4]));
endmodule

module Exercicio104 (
  input  Addr,
  input  R_W,
  input  CLK,
  input  CLR,
  input  [7:0] In,
  output [7:0] Out
);

  wire demultiplexer_1_out0, demultiplexer_1_out1;
  wire [3:0] exercicio102_1_out, exercicio102_2_out, exercicio102_3_out, exercicio102_4_out;

  Demultiplexer #(.enable("false")) demultiplexer_1 (
    .out0(demultiplexer_1_out0), .out1(demultiplexer_1_out1), .in(1'b1), .sel(Addr));
  Exercicio102 exercicio102_1 (
    .Addr(demultiplexer_1_out0), .R_W(R_W), .CLK(CLK), .In(In[3:0]), .Clr(CLR), .Out(exercicio102_1_out));
  Exercicio102 exercicio102_2 (
    .Addr(demultiplexer_1_out0), .R_W(R_W), .CLK(CLK), .In(In[7:4]), .Clr(CLR), .Out(exercicio102_2_out));
  Exercicio102 exercicio102_3 (
    .Addr(demultiplexer_1_out1), .R_W(R_W), .CLK(CLK), .In(In[3:0]), .Clr(CLR), .Out(exercicio102_3_out));
  Exercicio102 exercicio102_4 (
    .Addr(demultiplexer_1_out1), .R_W(R_W), .CLK(CLK), .In(In[7:4]), .Clr(CLR), .Out(exercicio102_4_out));
  Multiplexer #(.width(8), .enable("false")) multiplexer_1 (
    .in0({exercicio102_2_out, exercicio102_1_out}), .in1({exercicio102_4_out, exercicio102_3_out}),
    .out(Out), .sel(Addr));
endmodule

module Exercicio105 (
  input  [2:0] Addr,
  input  R_W,
  input  CLK,
  input  CLR,
  input  [7:0] In,
  output [7:0] Out
);

  wire demultiplexer_1_out0, demultiplexer_1_out1, demultiplexer_1_out2, demultiplexer_1_out3,
       demultiplexer_1_out4, demultiplexer_1_out5, demultiplexer_1_out6, demultiplexer_1_out7;
  wire [7:0] exercicio103_1_out, exercicio103_2_out, exercicio103_3_out, exercicio103_4_out,
       exercicio103_5_out, exercicio103_6_out, exercicio103_7_out, exercicio103_8_out;

  Demultiplexer #(.select(3), .enable("false")) demultiplexer_1 (
    .out0(demultiplexer_1_out0), .out1(demultiplexer_1_out1), .out2(demultiplexer_1_out2),
    .out3(demultiplexer_1_out3), .out4(demultiplexer_1_out4), .out5(demultiplexer_1_out5),
    .out6(demultiplexer_1_out6), .out7(demultiplexer_1_out7), .in(1'b1), .sel(Addr));
  Exercicio103 exercicio103_1 (
    .Addr(demultiplexer_1_out0), .R_W(R_W), .Clk(CLK), .Clr(CLR), .In(In), .Out(exercicio103_1_out));
  Exercicio103 exercicio103_2 (
    .Addr(demultiplexer_1_out1), .R_W(R_W), .Clk(CLK), .Clr(CLR), .In(In), .Out(exercicio103_2_out));
  Exercicio103 exercicio103_3 (
    .Addr(demultiplexer_1_out2), .R_W(R_W), .Clk(CLK), .Clr(CLR), .In(In), .Out(exercicio103_3_out));
  Exercicio103 exercicio103_4 (
    .Addr(demultiplexer_1_out3), .R_W(R_W), .Clk(CLK), .Clr(CLR), .In(In), .Out(exercicio103_4_out));
  Exercicio103 exercicio103_5 (
    .Addr(demultiplexer_1_out4), .R_W(R_W), .Clk(CLK), .Clr(CLR), .In(In), .Out(exercicio103_5_out));
  Exercicio103 exercicio103_6 (
    .Addr(demultiplexer_1_out5), .R_W(R_W), .Clk(CLK), .Clr(CLR), .In(In), .Out(exercicio103_6_out));
  Exercicio103 exercicio103_7 (
    .Addr(demultiplexer_1_out6), .R_W(R_W), .Clk(CLK), .Clr(CLR), .In(In), .Out(exercicio103_7_out));
  Exercicio103 exercicio103_8 (
    .Addr(demultiplexer_1_out7), .R_W(R_W), .Clk(CLK), .Clr(CLR), .In(In), .Out(exercicio103_8_out));
  Multiplexer #(.select(3), .width(8), .enable("false")) multiplexer_1 (
    .in0(exercicio103_1_out), .in1(exercicio103_2_out), .in2(exercicio103_3_out), .in3(exercicio103_4_out),
    .in4(exercicio103_5_out), .in5(exercicio103_6_out), .in6(exercicio103_7_out), .in7(exercicio103_8_out),
    .out(Out), .sel(Addr));
endmodule

module Exercicio106 (
  input  Addr,
  input  R_W,
  input  CLK,
  input  CLR,
  input  [15:0] In,
  output [15:0] Out
);

  Exercicio103 exercicio103_1 (.Addr(Addr), .R_W(R_W), .Clk(CLK), .Clr(CLR), .In(In[7:0]), .Out(Out[7:0]));
  Exercicio103 exercicio103_2 (.Addr(Addr), .R_W(R_W), .Clk(CLK), .Clr(CLR), .In(In[15:8]), .Out(Out[15:8]));
endmodule

module Exercicio107 (
  input  [1:0] Addr,
  input  R_W,
  input  CLK,
  input  CLR,
  input  [7:0] In,
  output [7:0] Out
);

  wire demultiplexer_1_out0, demultiplexer_1_out1, demultiplexer_1_out2, demultiplexer_1_out3;
  wire [7:0] exercicio103_1_out, exercicio103_2_out, exercicio103_3_out, exercicio103_4_out;

  Demultiplexer #(.select(2), .enable("false")) demultiplexer_1 (
    .out0(demultiplexer_1_out0), .out1(demultiplexer_1_out1), .out2(demultiplexer_1_out2),
    .out3(demultiplexer_1_out3), .in(1'b1), .sel(Addr));
  Exercicio103 exercicio103_1 (
    .Addr(demultiplexer_1_out0), .R_W(R_W), .Clk(CLK), .Clr(CLR), .In(In), .Out(exercicio103_1_out));
  Exercicio103 exercicio103_2 (
    .Addr(demultiplexer_1_out1), .R_W(R_W), .Clk(CLK), .Clr(CLR), .In(In), .Out(exercicio103_2_out));
  Exercicio103 exercicio103_3 (
    .Addr(demultiplexer_1_out2), .R_W(R_W), .Clk(CLK), .Clr(CLR), .In(In), .Out(exercicio103_3_out));
  Exercicio103 exercicio103_4 (
    .Addr(demultiplexer_1_out3), .R_W(R_W), .Clk(CLK), .Clr(CLR), .In(In), .Out(exercicio103_4_out));
  Multiplexer #(.select(2), .width(8), .enable("false")) multiplexer_1 (
    .in0(exercicio103_1_out), .in1(exercicio103_2_out), .in2(exercicio103_3_out), .in3(exercicio103_4_out),
    .out(Out), .sel(Addr));
endmodule
