// Logisim project Exercicios.circ as structural Verilog: 8 circuits, main circuit 1x1
// 1X1
module _1x1 (
  input  Addr,
  input  R_W,
  input  CLK,
  input  In,
  input  in_5,
  output out_6
);

  wire and_1_out, controlled_buffer_1_out, j_k_ff_1_q, not_1_out, not_2_out;

  and and_1 (and_1_out, Addr, R_W, CLK);
  not not_1 (not_1_out, CLK);
  assign controlled_buffer_1_out = not_1_out ? Addr : 1'bz;  // Controlled_Buffer controlled_buffer_1
  J_K_Flip_Flop j_k_ff_1 (
    .J(In), .clk(and_1_out), .K(not_2_out), .Q(j_k_ff_1_q), .reset(in_5));  // open: Qn, preset, en
  not not_2 (not_2_out, In);
  and and_2 (out_6, controlled_buffer_1_out, j_k_ff_1_q);

  // Notes on the sheet:
  //   Filipe Viana de Miranda -- 446415
endmodule

// 1X4
module Exercicio01 (
  input  Addr,
  input  R_W,
  input  CLK,
  input  [3:0] In,
  input  CLR,
  output [3:0] out_6
);

  _1x1 u_1x1_1 (.Addr(Addr), .R_W(R_W), .CLK(CLK), .In(In[0]), .in_5(CLR), .out_6(out_6[0]));
  _1x1 u_1x1_2 (.Addr(Addr), .R_W(R_W), .CLK(CLK), .In(In[1]), .in_5(CLR), .out_6(out_6[1]));
  _1x1 u_1x1_3 (.Addr(Addr), .R_W(R_W), .CLK(CLK), .In(In[2]), .in_5(CLR), .out_6(out_6[2]));
  _1x1 u_1x1_4 (.Addr(Addr), .R_W(R_W), .CLK(CLK), .In(In[3]), .in_5(CLR), .out_6(out_6[3]));

  // Notes on the sheet:
  //   Filipe Viana de Miranda -- 446415
endmodule

// 2x4
module Exercicio02 (
  input  Addr,
  input  R_W,
  input  CLK,
  input  [3:0] In,
  input  CLR,
  output [3:0] out_6
);

  wire demultiplexer_1_out0, demultiplexer_1_out1;
  wire [3:0] exercicio01_1_out_6, exercicio01_2_out_6;

  Demultiplexer #(.enable("false")) demultiplexer_1 (
    .out0(demultiplexer_1_out0), .out1(demultiplexer_1_out1), .in(1'b1), .sel(Addr));
  Exercicio01 exercicio01_1 (
    .Addr(demultiplexer_1_out0), .R_W(R_W), .CLK(CLK), .In(In), .CLR(CLR), .out_6(exercicio01_1_out_6));
  Exercicio01 exercicio01_2 (
    .Addr(demultiplexer_1_out1), .R_W(R_W), .CLK(CLK), .In(In), .CLR(CLR), .out_6(exercicio01_2_out_6));
  Multiplexer #(.width(4), .enable("false")) multiplexer_1 (
    .in0(exercicio01_1_out_6), .in1(exercicio01_2_out_6), .out(out_6), .sel(Addr));

  // Notes on the sheet:
  //   Filipe Viana de Miranda -- 446415
endmodule

// 1x8
module Exercicio03 (
  input  Addr,
  input  R_W,
  input  CLK,
  input  [7:0] In,
  input  CLR,
  output [7:0] out_6
);

  Exercicio01 exercicio01_1 (.Addr(Addr), .R_W(R_W), .CLK(CLK), .In(In[3:0]), .CLR(CLR), .out_6(out_6[3:0]));
  Exercicio01 exercicio01_2 (.Addr(Addr), .R_W(R_W), .CLK(CLK), .In(In[7:4]), .CLR(CLR), .out_6(out_6[7:4]));

  // Notes on the sheet:
  //   Filipe Viana de Miranda -- 446415
endmodule

module Exercicio04 (
  input  Addr,
  input  R_W,
  input  CLK,
  input  [7:0] In,
  input  CLR,
  output [7:0] out_6
);

  wire demultiplexer_1_out0, demultiplexer_1_out1;
  wire [7:0] exercicio03_1_out_6, exercicio03_2_out_6;

  Demultiplexer #(.enable("false")) demultiplexer_1 (
    .out0(demultiplexer_1_out0), .out1(demultiplexer_1_out1), .in(1'b1), .sel(Addr));
  Exercicio03 exercicio03_1 (
    .Addr(demultiplexer_1_out0), .R_W(R_W), .CLK(CLK), .In(In), .CLR(CLR), .out_6(exercicio03_1_out_6));
  Exercicio03 exercicio03_2 (
    .Addr(demultiplexer_1_out1), .R_W(R_W), .CLK(CLK), .In(In), .CLR(CLR), .out_6(exercicio03_2_out_6));
  Multiplexer #(.width(8), .enable("false")) multiplexer_1 (
    .in0(exercicio03_1_out_6), .in1(exercicio03_2_out_6), .out(out_6), .sel(Addr));

  // Notes on the sheet:
  //   Filipe Viana de Miranda -- 446415
endmodule

module Exercicio05 (
  input  [2:0] Addr,
  input  R_W,
  input  CLK,
  input  [7:0] In,
  input  CLR,
  output [7:0] out_6
);

  wire demultiplexer_1_out0, demultiplexer_1_out1, demultiplexer_1_out2, demultiplexer_1_out3,
       demultiplexer_1_out4, demultiplexer_1_out5, demultiplexer_1_out6, demultiplexer_1_out7;
  wire [7:0] exercicio03_1_out_6, exercicio03_2_out_6, exercicio03_3_out_6, exercicio03_4_out_6,
       exercicio03_5_out_6, exercicio03_6_out_6, exercicio03_7_out_6, exercicio03_8_out_6;

  Demultiplexer #(.select(3), .enable("false")) demultiplexer_1 (
    .out0(demultiplexer_1_out0), .out1(demultiplexer_1_out1), .out2(demultiplexer_1_out2),
    .out3(demultiplexer_1_out3), .out4(demultiplexer_1_out4), .out5(demultiplexer_1_out5),
    .out6(demultiplexer_1_out6), .out7(demultiplexer_1_out7), .in(1'b1), .sel(Addr));
  Exercicio03 exercicio03_1 (
    .Addr(demultiplexer_1_out0), .R_W(R_W), .CLK(CLK), .In(In), .CLR(CLR), .out_6(exercicio03_1_out_6));
  Exercicio03 exercicio03_2 (
    .Addr(demultiplexer_1_out1), .R_W(R_W), .CLK(CLK), .In(In), .CLR(CLR), .out_6(exercicio03_2_out_6));
  Exercicio03 exercicio03_3 (
    .Addr(demultiplexer_1_out2), .R_W(R_W), .CLK(CLK), .In(In), .CLR(CLR), .out_6(exercicio03_3_out_6));
  Exercicio03 exercicio03_4 (
    .Addr(demultiplexer_1_out3), .R_W(R_W), .CLK(CLK), .In(In), .CLR(CLR), .out_6(exercicio03_4_out_6));
  Exercicio03 exercicio03_5 (
    .Addr(demultiplexer_1_out4), .R_W(R_W), .CLK(CLK), .In(In), .CLR(CLR), .out_6(exercicio03_5_out_6));
  Exercicio03 exercicio03_6 (
    .Addr(demultiplexer_1_out5), .R_W(R_W), .CLK(CLK), .In(In), .CLR(CLR), .out_6(exercicio03_6_out_6));
  Multiplexer #(.select(3), .width(8), .enable("false")) multiplexer_1 (
    .in0(exercicio03_1_out_6), .in1(exercicio03_2_out_6), .in2(exercicio03_3_out_6),
    .in3(exercicio03_4_out_6), .in4(exercicio03_5_out_6), .in5(exercicio03_6_out_6),
    .in6(exercicio03_7_out_6), .in7(exercicio03_8_out_6), .out(out_6), .sel(Addr));
  Exercicio03 exercicio03_7 (
    .Addr(demultiplexer_1_out6), .R_W(CLK), .CLK(R_W), .In(In), .CLR(CLR), .out_6(exercicio03_7_out_6));
  Exercicio03 exercicio03_8 (
    .Addr(demultiplexer_1_out7), .R_W(R_W), .CLK(CLK), .In(In), .CLR(CLR), .out_6(exercicio03_8_out_6));

  // Notes on the sheet:
  //   Filipe Viana de Miranda -- 446415
endmodule

module Exercicio06 (
  input  Addr,
  input  R_W,
  input  CLK,
  input  [15:0] In,
  input  CLR,
  output [15:0] out_6
);

  Exercicio03 exercicio03_1 (.Addr(Addr), .R_W(R_W), .CLK(CLK), .In(In[7:0]), .CLR(CLR), .out_6(out_6[7:0]));
  Exercicio03 exercicio03_2 (.Addr(Addr), .R_W(R_W), .CLK(CLK), .In(In[15:8]), .CLR(CLR), .out_6(out_6[15:8]));

  // Notes on the sheet:
  //   Filipe Viana de Miranda -- 446415
endmodule

module Exercicio07 (
  input  [1:0] Addr,
  input  R_W,
  input  CLK,
  input  [7:0] In,
  input  CLR,
  output [7:0] out_6
);

  wire demultiplexer_1_out0, demultiplexer_1_out1, demultiplexer_1_out2, demultiplexer_1_out3;
  wire [7:0] exercicio03_1_out_6, exercicio03_2_out_6, exercicio03_3_out_6, exercicio03_4_out_6;

  Demultiplexer #(.select(2), .enable("false")) demultiplexer_1 (
    .out0(demultiplexer_1_out0), .out1(demultiplexer_1_out1), .out2(demultiplexer_1_out2),
    .out3(demultiplexer_1_out3), .in(1'b1), .sel(Addr));
  Exercicio03 exercicio03_1 (
    .Addr(demultiplexer_1_out0), .R_W(R_W), .CLK(CLK), .In(In), .CLR(CLR), .out_6(exercicio03_1_out_6));
  Exercicio03 exercicio03_2 (
    .Addr(demultiplexer_1_out1), .R_W(R_W), .CLK(CLK), .In(In), .CLR(CLR), .out_6(exercicio03_2_out_6));
  Exercicio03 exercicio03_3 (
    .Addr(demultiplexer_1_out2), .R_W(R_W), .CLK(CLK), .In(In), .CLR(CLR), .out_6(exercicio03_3_out_6));
  Exercicio03 exercicio03_4 (
    .Addr(demultiplexer_1_out3), .R_W(R_W), .CLK(CLK), .In(In), .CLR(CLR), .out_6(exercicio03_4_out_6));
  Multiplexer #(.select(2), .width(8), .enable("false")) multiplexer_1 (
    .in0(exercicio03_1_out_6), .in1(exercicio03_2_out_6), .in2(exercicio03_3_out_6),
    .in3(exercicio03_4_out_6), .out(out_6), .sel(Addr));

  // Notes on the sheet:
  //   Filipe Viana de Miranda -- 446415
endmodule
