// Logisim project Circuitos.circ as structural Verilog: 6 circuits, main circuit 1x1
module _1x1 (
  input  Address,
  input  R_W,
  input  CLK,
  input  IN,
  input  CLR,
  output OUT
);

  wire and_1_out, controlled_buffer_1_out, j_k_ff_1_q, not_1_out, not_2_out;

  assign controlled_buffer_1_out = not_2_out ? Address : 1'bz;  // Controlled_Buffer controlled_buffer_1
  and and_1 (and_1_out, Address, R_W, CLK);
  not not_1 (not_1_out, IN);
  not not_2 (not_2_out, CLK);
  and and_2 (OUT, controlled_buffer_1_out, j_k_ff_1_q);
  J_K_Flip_Flop j_k_ff_1 (.J(IN), .clk(and_1_out), .K(not_1_out), .Q(j_k_ff_1_q), .reset(CLR));  // open: Qn, preset, en

  // Notes on the sheet:
  //   Luhan Mairinck Reis   446987
endmodule

// 1x4
module Exercicio01 (
  input  Adress,
  input  R_W,
  input  CLK,
  input  [3:0] IN,
  input  CLR,
  output [3:0] out_6
);

  _1x1 u_1x1_1 (.Address(Adress), .R_W(R_W), .CLK(CLK), .IN(IN[0]), .CLR(CLR), .OUT(out_6[0]));
  _1x1 u_1x1_2 (.Address(Adress), .R_W(R_W), .CLK(CLK), .IN(IN[1]), .CLR(CLR), .OUT(out_6[1]));
  _1x1 u_1x1_3 (.Address(Adress), .R_W(R_W), .CLK(CLK), .IN(IN[2]), .CLR(CLR), .OUT(out_6[2]));
  _1x1 u_1x1_4 (.Address(Adress), .R_W(R_W), .CLK(CLK), .IN(IN[3]), .CLR(CLR), .OUT(out_6[3]));

  // Notes on the sheet:
  //   Luhan Mairinck Reis   446987
endmodule

// 2x4
module Exercicio02 (
  input  Adress,
  input  R_W,
  input  CLK,
  input  [3:0] IN,
  input  in_5,
  output [3:0] out_6
);

  wire demultiplexer_1_out0, demultiplexer_1_out1;
  wire [3:0] exercicio01_1_out_6, exercicio01_2_out_6;

  Demultiplexer #(.enable("false")) demultiplexer_1 (
    .out0(demultiplexer_1_out0), .out1(demultiplexer_1_out1), .in(1'b1), .sel(Adress));
  Exercicio01 exercicio01_1 (
    .Adress(demultiplexer_1_out0), .R_W(R_W), .CLK(CLK), .IN(IN), .CLR(in_5), .out_6(exercicio01_1_out_6));
  Exercicio01 exercicio01_2 (
    .Adress(demultiplexer_1_out1), .R_W(R_W), .CLK(CLK), .IN(IN), .CLR(in_5), .out_6(exercicio01_2_out_6));
  Multiplexer #(.width(4), .enable("false")) multiplexer_1 (
    .in0(exercicio01_1_out_6), .in1(exercicio01_2_out_6), .out(out_6), .sel(Adress));

  // Notes on the sheet:
  //   Luhan Mairinck Reis   446987
endmodule

// 1x8
module Exercicio03 (
  input  Adress,
  input  R_W,
  input  CLK,
  input  [7:0] IN,
  input  CLR,
  output [7:0] OUT
);

  Exercicio01 exercicio01_1 (.Adress(Adress), .R_W(R_W), .CLK(CLK), .IN(IN[3:0]), .CLR(CLR), .out_6(OUT[3:0]));
  Exercicio01 exercicio01_2 (.Adress(Adress), .R_W(R_W), .CLK(CLK), .IN(IN[7:4]), .CLR(CLR), .out_6(OUT[7:4]));

  // Notes on the sheet:
  //   Luhan Mairinck Reis   446987
endmodule

// 2x8
module Exercicio04 (
  input  Adress,
  input  R_W,
  input  CLK,
  input  [7:0] IN,
  input  CLR,
  output [7:0] OUT
);

  wire demultiplexer_1_out0, demultiplexer_1_out1;
  wire [3:0] exercicio02_1_out_6, exercicio02_2_out_6, exercicio02_3_out_6, exercicio02_4_out_6;

  Demultiplexer #(.enable("false")) demultiplexer_1 (
    .out0(demultiplexer_1_out0), .out1(demultiplexer_1_out1), .in(1'b1), .sel(Adress));
  Exercicio02 exercicio02_1 (
    .Adress(demultiplexer_1_out0), .R_W(R_W), .CLK(CLK), .IN(IN[3:0]), .in_5(CLR), .out_6(exercicio02_1_out_6));
  Exercicio02 exercicio02_2 (
    .Adress(demultiplexer_1_out0), .R_W(R_W), .CLK(CLK), .IN(IN[7:4]), .in_5(CLR), .out_6(exercicio02_2_out_6));
  Exercicio02 exercicio02_3 (
    .Adress(demultiplexer_1_out1), .R_W(R_W), .CLK(CLK), .IN(IN[3:0]), .in_5(CLR), .out_6(exercicio02_3_out_6));
  Exercicio02 exercicio02_4 (
    .Adress(demultiplexer_1_out1), .R_W(R_W), .CLK(CLK), .IN(IN[7:4]), .in_5(CLR), .out_6(exercicio02_4_out_6));
  Multiplexer #(.width(8), .enable("false")) multiplexer_1 (
    .in0({exercicio02_2_out_6, exercicio02_1_out_6}), .in1({exercicio02_4_out_6, exercicio02_3_out_6}),
    .out(OUT), .sel(Adress));

  // Notes on the sheet:
  //   Luhan Mairinck Reis   446987
endmodule

module Exercicio05 (
  input  [2:0] Adress,
  input  R_W,
  input  CLK,
  input  [7:0] OUT,
  input  [7:0] IN,
  input  CLR
);

  wire demultiplexer_1_out0, demultiplexer_1_out1, demultiplexer_1_out2, demultiplexer_1_out3,
       demultiplexer_1_out4, demultiplexer_1_out5, demultiplexer_1_out6, demultiplexer_1_out7;
  wire [7:0] exercicio03_1_out, exercicio03_2_out, exercicio03_3_out, exercicio03_4_out, exercicio03_5_out,
       exercicio03_6_out, exercicio03_7_out, exercicio03_8_out;

  Demultiplexer #(.select(3), .enable("false")) demultiplexer_1 (
    .out0(demultiplexer_1_out0), .out1(demultiplexer_1_out1), .out2(demultiplexer_1_out2),
    .out3(demultiplexer_1_out3), .out4(demultiplexer_1_out4), .out5(demultiplexer_1_out5),
    .out6(demultiplexer_1_out6), .out7(demultiplexer_1_out7), .in(1'b1), .sel(Adress));
  Exercicio03 exercicio03_1 (
    .Adress(demultiplexer_1_out0), .R_W(R_W), .CLK(CLK), .IN(IN), .CLR(CLR), .OUT(exercicio03_1_out));
  Exercicio03 exercicio03_2 (
    .Adress(demultiplexer_1_out1), .R_W(R_W), .CLK(CLK), .IN(IN), .CLR(CLR), .OUT(exercicio03_2_out));
  Exercicio03 exercicio03_3 (
    .Adress(demultiplexer_1_out2), .R_W(R_W), .CLK(CLK), .IN(IN), .CLR(CLR), .OUT(exercicio03_3_out));
  Exercicio03 exercicio03_4 (
    .Adress(demultiplexer_1_out3), .R_W(R_W), .CLK(CLK), .IN(IN), .CLR(CLR), .OUT(exercicio03_4_out));
  Exercicio03 exercicio03_5 (
    .Adress(demultiplexer_1_out4), .R_W(R_W), .CLK(CLK), .IN(IN), .CLR(CLR), .OUT(exercicio03_5_out));
  Exercicio03 exercicio03_6 (
    .Adress(demultiplexer_1_out5), .R_W(R_W), .CLK(CLK), .IN(IN), .CLR(CLR), .OUT(exercicio03_6_out));
  Exercicio03 exercicio03_7 (
    .Adress(demultiplexer_1_out6), .R_W(R_W), .CLK(CLK), .IN(IN), .CLR(CLR), .OUT(exercicio03_7_out));
  Exercicio03 exercicio03_8 (
    .Adress(demultiplexer_1_out7), .R_W(R_W), .CLK(CLK), .IN(IN), .CLR(CLR), .OUT(exercicio03_8_out));
  Multiplexer #(.select(3), .width(8), .enable("false")) multiplexer_1 (
    .in0(exercicio03_1_out), .in1(exercicio03_2_out), .in2(exercicio03_3_out), .in3(exercicio03_4_out),
    .in4(exercicio03_5_out), .in5(exercicio03_6_out), .in6(exercicio03_7_out), .in7(exercicio03_8_out),
    .out(OUT), .sel(Adress));

  // Notes on the sheet:
  //   Luhan Mairinck Reis   446987
endmodule
