// Logisim project Ex01.circ as structural Verilog: 2 circuits, main circuit 1x1
module _1x1 (
  input  addr,
  input  RW,
  input  CLK,
  input  IN,
  input  CLR,
  output OUT
);

  wire and_1_out, controlled_buffer_1_out, j_k_ff_1_q, not_1_out, not_2_out;

  and and_1 (and_1_out, addr, RW, CLK);
  not not_1 (not_1_out, CLK);
  assign controlled_buffer_1_out = not_1_out ? addr : 1'bz;  // Controlled_Buffer controlled_buffer_1
  J_K_Flip_Flop j_k_ff_1 (.J(IN), .clk(and_1_out), .K(not_2_out), .Q(j_k_ff_1_q), .reset(CLR));  // open: Qn, preset, en
  not not_2 (not_2_out, IN);
  and and_2 (OUT, controlled_buffer_1_out, j_k_ff_1_q);
endmodule

module main (
  input  ADDr,
  input  R_W,
  input  CLK,
  input  IN0,
  input  IN1,
  input  IN2,
  input  IN3,
  input  CLR,
  output out_9,
  output out_10,
  output out_11,
  output out_12
);

  _1x1 u_1x1_1 (.addr(ADDr), .RW(R_W), .CLK(CLK), .IN(IN0), .CLR(CLR), .OUT(out_9));
  _1x1 u_1x1_2 (.addr(ADDr), .RW(R_W), .CLK(CLK), .IN(IN1), .CLR(CLR), .OUT(out_10));
  _1x1 u_1x1_3 (.addr(ADDr), .RW(R_W), .CLK(CLK), .IN(IN2), .CLR(CLR), .OUT(out_11));
  _1x1 u_1x1_4 (.addr(ADDr), .RW(R_W), .CLK(CLK), .IN(IN3), .CLR(CLR), .OUT(out_12));
endmodule
