// Logisim project Ex04.circ as structural Verilog: 6 circuits, main circuit 1x1
module _1x1 (
  input  addr,
  input  RW,
  input  CLK,
  input  IN,
  input  CLR,
  output OUT
);

  wire and_1_out, controlled_buffer_1_out, j_k_ff_1_q, not_1_out, not_2_out;

  and and_1 (and_1_out, addr, RW, CLK);
  not not_1 (not_1_out, CLK);
  assign controlled_buffer_1_out = not_1_out ? addr : 1'bz;  // Controlled_Buffer controlled_buffer_1
  J_K_Flip_Flop j_k_ff_1 (.J(IN), .clk(and_1_out), .K(not_2_out), .Q(j_k_ff_1_q), .reset(CLR));  // open: Qn, preset, en
  not not_2 (not_2_out, IN);
  and and_2 (OUT, controlled_buffer_1_out, j_k_ff_1_q);
endmodule

module _1x4 (
  input  ADDr,
  input  R_W,
  input  CLK,
  input  [3:0] IN,
  input  CLR,
  output [3:0] OUT
);

  _1x1 u_1x1_1 (.addr(ADDr), .RW(R_W), .CLK(CLK), .IN(IN[0]), .CLR(CLR), .OUT(OUT[0]));
  _1x1 u_1x1_2 (.addr(ADDr), .RW(R_W), .CLK(CLK), .IN(IN[1]), .CLR(CLR), .OUT(OUT[1]));
  _1x1 u_1x1_3 (.addr(ADDr), .RW(R_W), .CLK(CLK), .IN(IN[2]), .CLR(CLR), .OUT(OUT[2]));
  _1x1 u_1x1_4 (.addr(ADDr), .RW(R_W), .CLK(CLK), .IN(IN[3]), .CLR(CLR), .OUT(OUT[3]));
endmodule

module _2x4 (
  input  ADDR,
  input  RW,
  input  CLK,
  input  [3:0] IN,
  input  CLR,
  output [3:0] OUT
);

  wire demultiplexer_1_out0, demultiplexer_1_out1;
  wire [3:0] n1x4_1_out, n1x4_2_out;

  Demultiplexer #(.enable("false")) demultiplexer_1 (
    .out0(demultiplexer_1_out0), .out1(demultiplexer_1_out1), .in(1'b1), .sel(ADDR));
  _1x4 u_1x4_1 (.ADDr(demultiplexer_1_out0), .R_W(RW), .CLK(CLK), .IN(IN), .CLR(CLR), .OUT(n1x4_1_out));
  _1x4 u_1x4_2 (.ADDr(demultiplexer_1_out1), .R_W(RW), .CLK(CLK), .IN(IN), .CLR(CLR), .OUT(n1x4_2_out));
  Multiplexer #(.width(4), .enable("false")) multiplexer_1 (.in0(n1x4_1_out), .in1(n1x4_2_out), .out(OUT), .sel(ADDR));
endmodule

module _1x8 (
  input  ADDR,
  input  RW,
  input  CLK,
  input  [7:0] IN,
  input  CLR,
  output [7:0] OUT
);

  _1x4 u_1x4_1 (.ADDr(ADDR), .R_W(RW), .CLK(CLK), .IN(IN[3:0]), .CLR(CLR), .OUT(OUT[3:0]));
  _1x4 u_1x4_2 (.ADDr(ADDR), .R_W(RW), .CLK(CLK), .IN(IN[7:4]), .CLR(CLR), .OUT(OUT[7:4]));
endmodule

module main (
  input  ADDR,
  input  RW,
  input  CLK,
  input  [7:0] IN,
  input  CLR,
  output [7:0] OUT
);

  wire demultiplexer_1_out0, demultiplexer_1_out1;
  wire [7:0] n1x8_1_out, n1x8_2_out;

  Demultiplexer #(.enable("false")) demultiplexer_1 (
    .out0(demultiplexer_1_out0), .out1(demultiplexer_1_out1), .in(1'b1), .sel(ADDR));
  _1x8 u_1x8_1 (.ADDR(demultiplexer_1_out0), .RW(RW), .CLK(CLK), .IN(IN), .CLR(CLR), .OUT(n1x8_1_out));
  _1x8 u_1x8_2 (.ADDR(demultiplexer_1_out1), .RW(RW), .CLK(CLK), .IN(IN), .CLR(CLR), .OUT(n1x8_2_out));
  Multiplexer #(.width(8), .enable("false")) multiplexer_1 (.in0(n1x8_1_out), .in1(n1x8_2_out), .out(OUT), .sel(ADDR));
endmodule

module test (
  input  ADDR,
  input  RW,
  input  CLK,
  input  [7:0] IN,
  input  CLR,
  output [7:0] OUT
);

  wire demultiplexer_1_out0, demultiplexer_1_out1;
  wire [3:0] n2x4_1_out, n2x4_2_out, n2x4_3_out, n2x4_4_out;

  Demultiplexer #(.enable("false")) demultiplexer_1 (
    .out0(demultiplexer_1_out0), .out1(demultiplexer_1_out1), .in(1'b1), .sel(ADDR));
  _2x4 u_2x4_1 (.ADDR(demultiplexer_1_out0), .RW(RW), .CLK(CLK), .IN(IN[3:0]), .CLR(CLR), .OUT(n2x4_1_out));
  _2x4 u_2x4_2 (.ADDR(demultiplexer_1_out0), .RW(RW), .CLK(CLK), .IN(IN[3:0]), .CLR(CLR), .OUT(n2x4_2_out));
  _2x4 u_2x4_3 (.ADDR(demultiplexer_1_out1), .RW(RW), .CLK(CLK), .IN(IN[7:4]), .CLR(CLR), .OUT(n2x4_3_out));
  _2x4 u_2x4_4 (.ADDR(demultiplexer_1_out1), .RW(RW), .CLK(CLK), .IN(IN[7:4]), .CLR(CLR), .OUT(n2x4_4_out));
  Multiplexer #(.width(8), .enable("false")) multiplexer_1 (
    .in0({n2x4_3_out, n2x4_1_out}), .in1({n2x4_4_out, n2x4_2_out}), .out(OUT), .sel(ADDR));
endmodule
