// Logisim project Ex07.circ as structural Verilog: 8 circuits, main circuit 1x1
module _1x1 (
  input  addr,
  input  RW,
  input  CLK,
  input  IN,
  input  CLR,
  output OUT
);

  wire and_1_out, controlled_buffer_1_out, j_k_ff_1_q, not_1_out, not_2_out;

  and and_1 (and_1_out, addr, RW, CLK);
  not not_1 (not_1_out, CLK);
  assign controlled_buffer_1_out = not_1_out ? addr : 1'bz;  // Controlled_Buffer controlled_buffer_1
  J_K_Flip_Flop j_k_ff_1 (.J(IN), .clk(and_1_out), .K(not_2_out), .Q(j_k_ff_1_q), .reset(CLR));  // open: Qn, preset, en
  not not_2 (not_2_out, IN);
  and and_2 (OUT, controlled_buffer_1_out, j_k_ff_1_q);
endmodule

module _1x4 (
  input  ADDr,
  input  R_W,
  input  CLK,
  input  [3:0] IN,
  input  CLR,
  output [3:0] OUT
);

  _1x1 u_1x1_1 (.addr(ADDr), .RW(R_W), .CLK(CLK), .IN(IN[0]), .CLR(CLR), .OUT(OUT[0]));
  _1x1 u_1x1_2 (.addr(ADDr), .RW(R_W), .CLK(CLK), .IN(IN[1]), .CLR(CLR), .OUT(OUT[1]));
  _1x1 u_1x1_3 (.addr(ADDr), .RW(R_W), .CLK(CLK), .IN(IN[2]), .CLR(CLR), .OUT(OUT[2]));
  _1x1 u_1x1_4 (.addr(ADDr), .RW(R_W), .CLK(CLK), .IN(IN[3]), .CLR(CLR), .OUT(OUT[3]));
endmodule

module _2x4 (
  input  ADDR,
  input  RW,
  input  CLK,
  input  [3:0] IN,
  input  CLR,
  output [3:0] OUT
);

  wire demultiplexer_1_out0, demultiplexer_1_out1;
  wire [3:0] n1x4_1_out, n1x4_2_out;

  Demultiplexer #(.enable("false")) demultiplexer_1 (
    .out0(demultiplexer_1_out0), .out1(demultiplexer_1_out1), .in(1'b1), .sel(ADDR));
  _1x4 u_1x4_1 (.ADDr(demultiplexer_1_out0), .R_W(RW), .CLK(CLK), .IN(IN), .CLR(CLR), .OUT(n1x4_1_out));
  _1x4 u_1x4_2 (.ADDr(demultiplexer_1_out1), .R_W(RW), .CLK(CLK), .IN(IN), .CLR(CLR), .OUT(n1x4_2_out));
  Multiplexer #(.width(4), .enable("false")) multiplexer_1 (.in0(n1x4_1_out), .in1(n1x4_2_out), .out(OUT), .sel(ADDR));
endmodule

module _1x8 (
  input  ADDR,
  input  RW,
  input  CLK,
  input  [7:0] IN,
  input  CLR,
  output [7:0] OUT
);

  _1x4 u_1x4_1 (.ADDr(ADDR), .R_W(RW), .CLK(CLK), .IN(IN[3:0]), .CLR(CLR), .OUT(OUT[3:0]));
  _1x4 u_1x4_2 (.ADDr(ADDR), .R_W(RW), .CLK(CLK), .IN(IN[7:4]), .CLR(CLR), .OUT(OUT[7:4]));
endmodule

module _2x8 (
  input  ADDR,
  input  RW,
  input  CLK,
  input  [7:0] IN,
  input  CLR,
  output [7:0] OUT
);

  wire demultiplexer_1_out0, demultiplexer_1_out1;
  wire [7:0] n1x8_1_out, n1x8_2_out;

  Demultiplexer #(.enable("false")) demultiplexer_1 (
    .out0(demultiplexer_1_out0), .out1(demultiplexer_1_out1), .in(1'b1), .sel(ADDR));
  _1x8 u_1x8_1 (.ADDR(demultiplexer_1_out0), .RW(RW), .CLK(CLK), .IN(IN), .CLR(CLR), .OUT(n1x8_1_out));
  _1x8 u_1x8_2 (.ADDR(demultiplexer_1_out1), .RW(RW), .CLK(CLK), .IN(IN), .CLR(CLR), .OUT(n1x8_2_out));
  Multiplexer #(.width(8), .enable("false")) multiplexer_1 (.in0(n1x8_1_out), .in1(n1x8_2_out), .out(OUT), .sel(ADDR));
endmodule

module _8x8 (
  input  [2:0] ADDR,
  input  RW,
  input  CLK,
  input  [7:0] IN,
  input  CLR,
  output [7:0] OUT
);

  wire demultiplexer_1_out0, demultiplexer_1_out1, demultiplexer_1_out2, demultiplexer_1_out3,
       demultiplexer_1_out4, demultiplexer_1_out5, demultiplexer_1_out6, demultiplexer_1_out7;
  wire [7:0] n1x8_1_out, n1x8_2_out, n1x8_3_out, n1x8_4_out, n1x8_5_out, n1x8_6_out, n1x8_7_out, n1x8_8_out;

  Demultiplexer #(.select(3), .enable("false")) demultiplexer_1 (
    .out0(demultiplexer_1_out0), .out1(demultiplexer_1_out1), .out2(demultiplexer_1_out2),
    .out3(demultiplexer_1_out3), .out4(demultiplexer_1_out4), .out5(demultiplexer_1_out5),
    .out6(demultiplexer_1_out6), .out7(demultiplexer_1_out7), .in(1'b1), .sel(ADDR));
  _1x8 u_1x8_1 (.ADDR(demultiplexer_1_out0), .RW(RW), .CLK(CLK), .IN(IN), .CLR(CLR), .OUT(n1x8_1_out));
  _1x8 u_1x8_2 (.ADDR(demultiplexer_1_out1), .RW(RW), .CLK(CLK), .IN(IN), .CLR(CLR), .OUT(n1x8_2_out));
  _1x8 u_1x8_3 (.ADDR(demultiplexer_1_out2), .RW(RW), .CLK(CLK), .IN(IN), .CLR(CLR), .OUT(n1x8_3_out));
  _1x8 u_1x8_4 (.ADDR(demultiplexer_1_out3), .RW(RW), .CLK(CLK), .IN(IN), .CLR(CLR), .OUT(n1x8_4_out));
  _1x8 u_1x8_5 (.ADDR(demultiplexer_1_out4), .RW(RW), .CLK(CLK), .IN(IN), .CLR(CLR), .OUT(n1x8_5_out));
  _1x8 u_1x8_6 (.ADDR(demultiplexer_1_out5), .RW(RW), .CLK(CLK), .IN(IN), .CLR(CLR), .OUT(n1x8_6_out));
  _1x8 u_1x8_7 (.ADDR(demultiplexer_1_out6), .RW(RW), .CLK(CLK), .IN(IN), .CLR(CLR), .OUT(n1x8_7_out));
  _1x8 u_1x8_8 (.ADDR(demultiplexer_1_out7), .RW(RW), .CLK(CLK), .IN(IN), .CLR(CLR), .OUT(n1x8_8_out));
  Multiplexer #(.select(3), .width(8), .enable("false")) multiplexer_1 (
    .in0(n1x8_1_out), .in1(n1x8_2_out), .in2(n1x8_3_out), .in3(n1x8_4_out), .in4(n1x8_5_out),
    .in5(n1x8_6_out), .in6(n1x8_7_out), .in7(n1x8_8_out), .out(OUT), .sel(ADDR));
endmodule

module _1x16 (
  input  ADDR,
  input  RW,
  input  CLK,
  input  [15:0] IN,
  input  CLR,
  output [15:0] OUT
);

  _1x8 u_1x8_1 (.ADDR(ADDR), .RW(RW), .CLK(CLK), .IN(IN[7:0]), .CLR(CLR), .OUT(OUT[7:0]));
  _1x8 u_1x8_2 (.ADDR(ADDR), .RW(RW), .CLK(CLK), .IN(IN[15:8]), .CLR(CLR), .OUT(OUT[15:8]));
endmodule

module main (
  input  [1:0] ADDR,
  input  RW,
  input  CLK,
  input  [7:0] IN,
  input  CLR,
  output [7:0] OUT
);

  wire demultiplexer_1_out0, demultiplexer_1_out1, demultiplexer_1_out2, demultiplexer_1_out3;
  wire [7:0] n1x8_1_out, n1x8_2_out, n1x8_3_out, n1x8_4_out;

  Demultiplexer #(.select(2), .enable("false")) demultiplexer_1 (
    .out0(demultiplexer_1_out0), .out1(demultiplexer_1_out1), .out2(demultiplexer_1_out2),
    .out3(demultiplexer_1_out3), .in(1'b1), .sel(ADDR));
  _1x8 u_1x8_1 (.ADDR(demultiplexer_1_out0), .RW(RW), .CLK(CLK), .IN(IN), .CLR(CLR), .OUT(n1x8_1_out));
  _1x8 u_1x8_2 (.ADDR(demultiplexer_1_out1), .RW(RW), .CLK(CLK), .IN(IN), .CLR(CLR), .OUT(n1x8_2_out));
  _1x8 u_1x8_3 (.ADDR(demultiplexer_1_out2), .RW(RW), .CLK(CLK), .IN(IN), .CLR(CLR), .OUT(n1x8_3_out));
  _1x8 u_1x8_4 (.ADDR(demultiplexer_1_out3), .RW(RW), .CLK(CLK), .IN(IN), .CLR(CLR), .OUT(n1x8_4_out));
  Multiplexer #(.select(2), .width(8), .enable("false")) multiplexer_1 (
    .in0(n1x8_1_out), .in1(n1x8_2_out), .in2(n1x8_3_out), .in3(n1x8_4_out), .out(OUT), .sel(ADDR));
endmodule
