// Logisim project Exercicio002.circ as structural Verilog: 4 circuits, main circuit main
module main (
  input  [3:0] Input,
  input  Address,
  input  read_write,
  input  Clock,
  input  clear,
  output [3:0] Output
);

  wire not_1_out;
  wire [3:0] R1_output, R2_output, SA_chave_posicao_0, SA_chave_posicao_1;

  SeletorDeRAMs SA (
    .\input (Input), .address(Address), .chave_posicao_0(SA_chave_posicao_0),
    .chave_posicao_1(SA_chave_posicao_1));
  not not_1 (not_1_out, Address);
  RAM1X4 R1 (
    .data(SA_chave_posicao_0), .Address(not_1_out), .read_write(read_write), .Clock(Clock), .Clear(clear),
    .\output (R1_output));
  RAM1X4 R2 (
    .data(SA_chave_posicao_1), .Address(Address), .read_write(read_write), .Clock(Clock), .Clear(clear),
    .\output (R2_output));
  deseletorDeRAMs SB (
    .Addres_na_posicao_0(R1_output), .Addres_na_possicao_1(R2_output), .in_3(Address), .Output(Output));
endmodule

// RAM
module RAM1X4 (
  input  [3:0] data,
  input  Address,
  input  read_write,
  input  Clock,
  input  Clear,
  output [3:0] \output 
);

  wire E_out, N0_out, N1_out, N2_out, N3_out;
  wire [3:0] D_q;

  and E (E_out, Address, read_write, Clock);
  not N0 (N0_out, data[3]);
  J_K_Flip_Flop A (.J(data[3]), .clk(E_out), .K(N0_out), .Q(D_q[3]), .reset(Clear));  // open: Qn, preset, en
  not N1 (N1_out, data[2]);
  J_K_Flip_Flop B (.J(data[2]), .clk(E_out), .K(N1_out), .Q(D_q[2]), .reset(Clear));  // open: Qn, preset, en
  not N2 (N2_out, data[1]);
  J_K_Flip_Flop C (.J(data[1]), .clk(E_out), .K(N2_out), .Q(D_q[1]), .reset(Clear));  // open: Qn, preset, en
  not N3 (N3_out, data[0]);
  assign \output  = {4{Address}} & D_q;  // AND_Gate F, 4 bits wide
  J_K_Flip_Flop D (.J(data[0]), .clk(E_out), .K(N3_out), .Q(D_q[0]), .reset(Clear));  // open: Qn, preset, en
endmodule

module SeletorDeRAMs (
  input  [3:0] \input ,
  input  address,
  output [3:0] chave_posicao_0,
  output [3:0] chave_posicao_1
);

  wire [3:0] N_out;

  assign N_out = ~{4{address}};  // NOT_Gate N, 4 bits wide
  assign chave_posicao_0 = N_out & \input ;  // AND_Gate A, 4 bits wide
  assign chave_posicao_1 = \input  & {4{address}};  // AND_Gate B, 4 bits wide
endmodule

module deseletorDeRAMs (
  input  [3:0] Addres_na_posicao_0,
  input  [3:0] Addres_na_possicao_1,
  input  in_3,
  output [3:0] Output
);

  wire [3:0] A_out, B_out, N_out;

  assign A_out = Addres_na_posicao_0 & N_out;  // AND_Gate A, 4 bits wide
  assign N_out = ~{4{in_3}};  // NOT_Gate N, 4 bits wide
  assign B_out = Addres_na_possicao_1 & {4{in_3}};  // AND_Gate B, 4 bits wide
  assign Output = A_out | B_out;  // OR_Gate C, 4 bits wide
endmodule
