// Logisim project Exercicio004.circ as structural Verilog: 4 circuits, main circuit main
module main (
  input  [7:0] \input ,
  input  ADDR,
  input  R_W,
  input  CLK,
  input  CLR,
  output [7:0] \output 
);

  wire demultiplexer_1_out0, demultiplexer_1_out1;
  wire [3:0] ram2x4_1_output, ram2x4_2_output, ram2x4_3_output, ram2x4_4_output;

  Demultiplexer demultiplexer_1 (
    .out0(demultiplexer_1_out0), .out1(demultiplexer_1_out1), .in(1'b1), .sel(ADDR));  // open: en
  RAM2X4 ram2x4_1 (
    .Input(\input [3:0]), .Address(demultiplexer_1_out0), .read_write(R_W), .Clock(CLK), .clear(CLR),
    .Output(ram2x4_1_output));
  RAM2X4 ram2x4_2 (
    .Input(\input [7:4]), .Address(demultiplexer_1_out0), .read_write(R_W), .Clock(CLK), .clear(CLR),
    .Output(ram2x4_2_output));
  RAM2X4 ram2x4_3 (
    .Input(\input [3:0]), .Address(demultiplexer_1_out1), .read_write(R_W), .Clock(CLK), .clear(CLR),
    .Output(ram2x4_3_output));
  RAM2X4 ram2x4_4 (
    .Input(\input [7:4]), .Address(demultiplexer_1_out1), .read_write(R_W), .Clock(CLK), .clear(CLR),
    .Output(ram2x4_4_output));
  Multiplexer #(.width(8)) multiplexer_1 (
    .in0({ram2x4_2_output, ram2x4_1_output}), .in1({ram2x4_4_output, ram2x4_3_output}), .out(\output ),
    .sel(ADDR));  // open: en
endmodule

module RAM1X4 (
  input  [3:0] data,
  input  Address,
  input  read_write,
  input  Clock,
  input  Clear,
  output [3:0] \output 
);

  wire E_out, N0_out, N1_out, N2_out, N3_out;
  wire [3:0] D_q;

  and E (E_out, Address, read_write, Clock);
  not N0 (N0_out, data[3]);
  J_K_Flip_Flop A (.J(data[3]), .clk(E_out), .K(N0_out), .Q(D_q[3]), .reset(Clear));  // open: Qn, preset, en
  not N1 (N1_out, data[2]);
  J_K_Flip_Flop B (.J(data[2]), .clk(E_out), .K(N1_out), .Q(D_q[2]), .reset(Clear));  // open: Qn, preset, en
  not N2 (N2_out, data[1]);
  J_K_Flip_Flop C (.J(data[1]), .clk(E_out), .K(N2_out), .Q(D_q[1]), .reset(Clear));  // open: Qn, preset, en
  not N3 (N3_out, data[0]);
  assign \output  = {4{Address}} & D_q;  // AND_Gate F, 4 bits wide
  J_K_Flip_Flop D (.J(data[0]), .clk(E_out), .K(N3_out), .Q(D_q[0]), .reset(Clear));  // open: Qn, preset, en
endmodule

// RAM1X8
module RAM1x8 (
  input  [7:0] \input ,
  input  Adress,
  input  read_write,
  input  clock,
  input  clear,
  output [7:0] \output 
);

  RAM1X4 ram1x4_1 (
    .data(\input [3:0]), .Address(Adress), .read_write(read_write), .Clock(clock), .Clear(clear),
    .\output (\output [3:0]));
  RAM1X4 ram1x4_2 (
    .data(\input [7:4]), .Address(Adress), .read_write(read_write), .Clock(clock), .Clear(clear),
    .\output (\output [7:4]));
endmodule

module RAM2X4 (
  input  [3:0] Input,
  input  Address,
  input  read_write,
  input  Clock,
  input  clear,
  output [3:0] Output
);

  wire demultiplexer_1_out0, demultiplexer_1_out1;
  wire [3:0] ram1x4_1_output, ram1x4_2_output;

  Demultiplexer demultiplexer_1 (
    .out0(demultiplexer_1_out0), .out1(demultiplexer_1_out1), .in(1'b1), .sel(Address));  // open: en
  RAM1X4 ram1x4_1 (
    .data(Input), .Address(demultiplexer_1_out0), .read_write(read_write), .Clock(Clock), .Clear(clear),
    .\output (ram1x4_1_output));
  RAM1X4 ram1x4_2 (
    .data(Input), .Address(demultiplexer_1_out1), .read_write(read_write), .Clock(Clock), .Clear(clear),
    .\output (ram1x4_2_output));
  Multiplexer #(.width(4)) multiplexer_1 (
    .in0(ram1x4_1_output), .in1(ram1x4_2_output), .out(Output), .sel(Address));  // open: en
endmodule
