// Logisim project Exercicio006.circ as structural Verilog: 3 circuits, main circuit main
module main (
  input  [15:0] in_1,
  input  in_2,
  input  in_3,
  input  in_4,
  input  in_5,
  output [15:0] out_6
);

  RAM1X8 ram1x8_1 (
    .\input (in_1[7:0]), .Adress(in_2), .read_write(in_3), .clock(in_4), .clear(in_5), .\output (out_6[7:0]));
  RAM1X8 ram1x8_2 (
    .\input (in_1[15:8]), .Adress(in_2), .read_write(in_3), .clock(in_4), .clear(in_5), .\output (out_6[15:8]));
endmodule

module RAM1X8 (
  input  [7:0] \input ,
  input  Adress,
  input  read_write,
  input  clock,
  input  clear,
  output [7:0] \output 
);

  RAM1X4 ram1x4_1 (
    .data(\input [3:0]), .Address(Adress), .read_write(read_write), .Clock(clock), .Clear(clear),
    .\output (\output [3:0]));
  RAM1X4 ram1x4_2 (
    .data(\input [7:4]), .Address(Adress), .read_write(read_write), .Clock(clock), .Clear(clear),
    .\output (\output [7:4]));
endmodule

module RAM1X4 (
  input  [3:0] data,
  input  Address,
  input  read_write,
  input  Clock,
  input  Clear,
  output [3:0] \output 
);

  wire E_out, N0_out, N1_out, N2_out, N3_out;
  wire [3:0] D_q;

  and E (E_out, Address, read_write, Clock);
  not N0 (N0_out, data[3]);
  J_K_Flip_Flop A (.J(data[3]), .clk(E_out), .K(N0_out), .Q(D_q[3]), .reset(Clear));  // open: Qn, preset, en
  not N1 (N1_out, data[2]);
  J_K_Flip_Flop B (.J(data[2]), .clk(E_out), .K(N1_out), .Q(D_q[2]), .reset(Clear));  // open: Qn, preset, en
  not N2 (N2_out, data[1]);
  J_K_Flip_Flop C (.J(data[1]), .clk(E_out), .K(N2_out), .Q(D_q[1]), .reset(Clear));  // open: Qn, preset, en
  not N3 (N3_out, data[0]);
  assign \output  = {4{Address}} & D_q;  // AND_Gate F, 4 bits wide
  J_K_Flip_Flop D (.J(data[0]), .clk(E_out), .K(N3_out), .Q(D_q[0]), .reset(Clear));  // open: Qn, preset, en
endmodule
