// Logisim project Circuitos.circ as structural Verilog: 8 circuits, main circuit main
module main (
);


  // Notes on the sheet:
  //   Circuitos Guia 10 - Ana Cristina - 427385
endmodule

// 1x4
module RAM_1x4 (
  input  Addr,
  input  clk,
  input  R_W,
  input  [3:0] \input ,
  input  clr,
  output [3:0] \output 
);

  wire and_1_out, j_k_ff_1_q, j_k_ff_2_q, j_k_ff_3_q, j_k_ff_4_q, not_1_out, not_2_out, not_3_out, not_4_out;

  and and_1 (and_1_out, Addr, clk, R_W);
  and and_2 (\output [3], Addr, j_k_ff_1_q);
  J_K_Flip_Flop j_k_ff_1 (
    .J(\input [3]), .clk(and_1_out), .K(not_1_out), .Q(j_k_ff_1_q), .reset(clr));  // open: Qn, preset, en
  not not_1 (not_1_out, \input [3]);
  and and_3 (\output [2], Addr, j_k_ff_2_q);
  J_K_Flip_Flop j_k_ff_2 (
    .J(\input [2]), .clk(and_1_out), .K(not_2_out), .Q(j_k_ff_2_q), .reset(clr));  // open: Qn, preset, en
  not not_2 (not_2_out, \input [2]);
  and and_4 (\output [1], Addr, j_k_ff_3_q);
  J_K_Flip_Flop j_k_ff_3 (
    .J(\input [1]), .clk(and_1_out), .K(not_3_out), .Q(j_k_ff_3_q), .reset(clr));  // open: Qn, preset, en
  not not_3 (not_3_out, \input [1]);
  not not_4 (not_4_out, \input [0]);
  and and_5 (\output [0], Addr, j_k_ff_4_q);
  J_K_Flip_Flop j_k_ff_4 (
    .J(\input [0]), .clk(and_1_out), .K(not_4_out), .Q(j_k_ff_4_q), .reset(clr));  // open: Qn, preset, en

  // Notes on the sheet:
  //   RAM 1x4 - Ana Cristina - 427385
endmodule

// 2x4
module RAM_2x4 (
  input  Addr,
  input  clk,
  input  R_W,
  input  [3:0] \input ,
  input  clr,
  output [3:0] \output 
);

  wire demultiplexer_1_out0, demultiplexer_1_out1;
  wire [3:0] ram_1x4_1_output, ram_1x4_2_output;

  Demultiplexer #(.enable("false")) demultiplexer_1 (
    .out0(demultiplexer_1_out0), .out1(demultiplexer_1_out1), .in(1'b1), .sel(Addr));
  RAM_1x4 ram_1x4_1 (
    .Addr(demultiplexer_1_out0), .clk(clk), .R_W(R_W), .\input (\input ), .\output (ram_1x4_1_output),
    .clr(clr));
  RAM_1x4 ram_1x4_2 (
    .Addr(demultiplexer_1_out1), .clk(clk), .R_W(R_W), .\input (\input ), .\output (ram_1x4_2_output),
    .clr(clr));
  Multiplexer #(.width(4), .enable("false")) multiplexer_1 (
    .in0(ram_1x4_1_output), .in1(ram_1x4_2_output), .out(\output ), .sel(Addr));

  // Notes on the sheet:
  //   RAM 2x4 - Ana Cristina - 427385
endmodule

// 1x8
module RAM_1x8 (
  input  Addr,
  input  clk,
  input  R_W,
  input  [7:0] \input ,
  input  clr,
  output [7:0] \output 
);

  RAM_1x4 ram_1x4_1 (.Addr(Addr), .clk(clk), .R_W(R_W), .\input (\input [3:0]), .\output (\output [3:0]), .clr(clr));
  RAM_1x4 ram_1x4_2 (.Addr(Addr), .clk(clk), .R_W(R_W), .\input (\input [7:4]), .\output (\output [7:4]), .clr(clr));

  // Notes on the sheet:
  //   RAM 1x8 - Ana Cristina - 427385
endmodule

module RAM_2x8 (
  input  Addr,
  input  clk,
  input  R_W,
  input  clr,
  input  [7:0] \input ,
  output [7:0] out_6
);

  RAM_2x4 ram_2x4_1 (.Addr(Addr), .clk(clk), .R_W(R_W), .\input (\input [7:4]), .clr(clr), .\output (out_6[7:4]));
  RAM_2x4 ram_2x4_2 (.Addr(Addr), .clk(clk), .R_W(R_W), .\input (\input [3:0]), .clr(clr), .\output (out_6[3:0]));

  // Notes on the sheet:
  //   RAM 2x8 - Ana Cristina - 427385
endmodule

module RAM_8x8 (
  input  [2:0] Addr,
  input  clk,
  input  R_W,
  input  clr,
  input  [7:0] \input ,
  output [7:0] out_6
);

  wire demultiplexer_1_out0, demultiplexer_1_out1, demultiplexer_1_out2, demultiplexer_1_out3,
       demultiplexer_1_out4, demultiplexer_1_out5, demultiplexer_1_out6, demultiplexer_1_out7;
  wire [7:0] ram_1x8_1_output, ram_1x8_2_output, ram_1x8_3_output, ram_1x8_4_output, ram_1x8_5_output,
       ram_1x8_6_output, ram_1x8_7_output, ram_1x8_8_output;

  Demultiplexer #(.select(3), .enable("false")) demultiplexer_1 (
    .out0(demultiplexer_1_out0), .out1(demultiplexer_1_out1), .out2(demultiplexer_1_out2),
    .out3(demultiplexer_1_out3), .out4(demultiplexer_1_out4), .out5(demultiplexer_1_out5),
    .out6(demultiplexer_1_out6), .out7(demultiplexer_1_out7), .in(1'b1), .sel(Addr));
  RAM_1x8 ram_1x8_1 (
    .Addr(demultiplexer_1_out0), .clk(clk), .R_W(R_W), .\input (\input ), .clr(clr),
    .\output (ram_1x8_1_output));
  RAM_1x8 ram_1x8_2 (
    .Addr(demultiplexer_1_out1), .clk(clk), .R_W(R_W), .\input (\input ), .clr(clr),
    .\output (ram_1x8_2_output));
  RAM_1x8 ram_1x8_3 (
    .Addr(demultiplexer_1_out2), .clk(clk), .R_W(R_W), .\input (\input ), .clr(clr),
    .\output (ram_1x8_3_output));
  RAM_1x8 ram_1x8_4 (
    .Addr(demultiplexer_1_out3), .clk(clk), .R_W(R_W), .\input (\input ), .clr(clr),
    .\output (ram_1x8_4_output));
  RAM_1x8 ram_1x8_5 (
    .Addr(demultiplexer_1_out4), .clk(clk), .R_W(R_W), .\input (\input ), .clr(clr),
    .\output (ram_1x8_5_output));
  RAM_1x8 ram_1x8_6 (
    .Addr(demultiplexer_1_out5), .clk(clk), .R_W(R_W), .\input (\input ), .clr(clr),
    .\output (ram_1x8_6_output));
  RAM_1x8 ram_1x8_7 (
    .Addr(demultiplexer_1_out6), .clk(clk), .R_W(R_W), .\input (\input ), .clr(clr),
    .\output (ram_1x8_7_output));
  RAM_1x8 ram_1x8_8 (
    .Addr(demultiplexer_1_out7), .clk(clk), .R_W(R_W), .\input (\input ), .clr(clr),
    .\output (ram_1x8_8_output));
  Multiplexer #(.select(3), .width(8), .enable("false")) multiplexer_1 (
    .in0(ram_1x8_1_output), .in1(ram_1x8_2_output), .in2(ram_1x8_3_output), .in3(ram_1x8_4_output),
    .in4(ram_1x8_5_output), .in5(ram_1x8_6_output), .in6(ram_1x8_7_output), .in7(ram_1x8_8_output),
    .out(out_6), .sel(Addr));

  // Notes on the sheet:
  //   RAM 8x8 - Ana Cristina - 427385
endmodule

module RAM_1x16 (
  input  Addr,
  input  clk,
  input  R_W,
  input  [15:0] \input ,
  output [15:0] out_5
);

  RAM_1x8 ram_1x8_1 (.Addr(Addr), .clk(clk), .R_W(R_W), .\input (\input [15:8]), .\output (out_5[15:8]));  // open: clr
  RAM_1x8 ram_1x8_2 (.Addr(Addr), .clk(clk), .R_W(R_W), .\input (\input [7:0]), .\output (out_5[7:0]));  // open: clr

  // Notes on the sheet:
  //   RAM 1x16 - Ana Cristina - 427385
endmodule

module RAM_4x8 (
  input  [1:0] Addr,
  input  clk,
  input  R_W,
  input  clr,
  input  [7:0] \input ,
  output [7:0] out_6
);

  wire demultiplexer_1_out0, demultiplexer_1_out1, demultiplexer_1_out2, demultiplexer_1_out3;
  wire [7:0] ram_1x8_1_output, ram_1x8_2_output, ram_1x8_3_output, ram_1x8_4_output;

  Demultiplexer #(.select(2), .enable("false")) demultiplexer_1 (
    .out0(demultiplexer_1_out0), .out1(demultiplexer_1_out1), .out2(demultiplexer_1_out2),
    .out3(demultiplexer_1_out3), .in(1'b1), .sel(Addr));
  RAM_1x8 ram_1x8_1 (
    .Addr(demultiplexer_1_out0), .clk(clk), .R_W(R_W), .\input (\input ), .clr(clr),
    .\output (ram_1x8_1_output));
  RAM_1x8 ram_1x8_2 (
    .Addr(demultiplexer_1_out1), .clk(clk), .R_W(R_W), .\input (\input ), .clr(clr),
    .\output (ram_1x8_2_output));
  RAM_1x8 ram_1x8_3 (
    .Addr(demultiplexer_1_out2), .clk(clk), .R_W(R_W), .\input (\input ), .clr(clr),
    .\output (ram_1x8_3_output));
  RAM_1x8 ram_1x8_4 (
    .Addr(demultiplexer_1_out3), .clk(clk), .R_W(R_W), .\input (\input ), .clr(clr),
    .\output (ram_1x8_4_output));
  Multiplexer #(.select(2), .width(8), .enable("false")) multiplexer_1 (
    .in0(ram_1x8_1_output), .in1(ram_1x8_2_output), .in2(ram_1x8_3_output), .in3(ram_1x8_4_output),
    .out(out_6), .sel(Addr));

  // Notes on the sheet:
  //   RAM 4x8 - Ana Cristina - 427385
endmodule
