// Logisim project Exemplo0053b.circ as structural Verilog: 1 circuit, main circuit main
module main (
  input  Clock,
  input  in_2,
  input  Reset,
  output out_4
);

  wire and_1_out, d_ff_1_q, d_ff_2_q, d_ff_2_qn, d_ff_3_q, d_ff_3_qn, d_ff_4_q, not_1_out, or_1_out;

  and and_1 (and_1_out, not_1_out, out_4);
  or or_1 (or_1_out, Reset, and_1_out);
  not not_1 (not_1_out, Clock);
  D_Flip_Flop d_ff_1 (.clk(Clock), .D(in_2), .Q(d_ff_1_q), .reset(or_1_out));  // open: Qn, preset, en
  D_Flip_Flop d_ff_2 (.clk(Clock), .D(d_ff_1_q), .Q(d_ff_2_q), .Qn(d_ff_2_qn), .reset(or_1_out));  // open: preset, en
  D_Flip_Flop d_ff_3 (.clk(Clock), .D(d_ff_2_q), .Q(d_ff_3_q), .Qn(d_ff_3_qn), .reset(or_1_out));  // open: preset, en
  D_Flip_Flop d_ff_4 (.clk(Clock), .D(d_ff_3_q), .Q(d_ff_4_q), .reset(or_1_out));  // open: Qn, preset, en
  and and_2 (out_4, d_ff_4_q, d_ff_3_qn, d_ff_2_qn, d_ff_1_q);

  // Notes on the sheet:
  //   Lucas Siqueira Chagas - 380783
endmodule
