// Logisim project exercicio05.circ as structural Verilog: 1 circuit, main circuit main
module main (
  input  in_1,
  input  in_2,
  input  in_3,
  input  in_4,
  input  in_5,
  input  in_6,
  input  in_7,
  output out_8,
  output out_9,
  output out_10,
  output out_11
);

  wire and_1_out, and_2_out, and_3_out, and_4_out, clock_1_out;

  Clock clock_1 (.out(clock_1_out));
  D_Flip_Flop d_ff_1 (.clk(clock_1_out), .D(in_1), .Q(out_8), .preset(and_1_out), .reset(in_2));  // open: Qn, en
  and and_1 (and_1_out, in_4, in_3);
  D_Flip_Flop d_ff_2 (.clk(clock_1_out), .D(out_8), .Q(out_9), .preset(and_2_out), .reset(in_2));  // open: Qn, en
  and and_2 (and_2_out, in_5, in_3);
  D_Flip_Flop d_ff_3 (.clk(clock_1_out), .D(out_9), .Q(out_10), .preset(and_3_out), .reset(in_2));  // open: Qn, en
  and and_3 (and_3_out, in_6, in_3);
  D_Flip_Flop d_ff_4 (.clk(clock_1_out), .D(out_10), .Q(out_11), .preset(and_4_out), .reset(in_2));  // open: Qn, en
  and and_4 (and_4_out, in_7, in_3);

  // Notes on the sheet:
  //   Lucas Siqueira Chagas - 380783
  //   paralelo para serial
endmodule
