// Logisim project Circuitos.circ as structural Verilog
// 1x4
module Memoria_1x4 (
  input  Addr,
  input  R_W,
  input  Clk,
  input  Clr,
  input  [3:0] In,
  output [3:0] Output
);

  wire and_1_out, j_k_ff_1_q, j_k_ff_2_q, j_k_ff_3_q, j_k_ff_4_q, not_1_out, not_2_out, not_3_out, not_4_out;

  and and_1 (and_1_out, Addr, R_W, Clk);
  and and_2 (Output[0], Addr, j_k_ff_1_q);
  J_K_Flip_Flop j_k_ff_1 (
    .J(In[0]), .clk(and_1_out), .K(not_1_out), .Q(j_k_ff_1_q), .reset(Clr));  // open: Qn, preset, en
  not not_1 (not_1_out, In[0]);
  and and_3 (Output[1], Addr, j_k_ff_2_q);
  J_K_Flip_Flop j_k_ff_2 (
    .J(In[1]), .clk(and_1_out), .K(not_2_out), .Q(j_k_ff_2_q), .reset(Clr));  // open: Qn, preset, en
  not not_2 (not_2_out, In[1]);
  and and_4 (Output[2], Addr, j_k_ff_3_q);
  not not_3 (not_3_out, In[2]);
  J_K_Flip_Flop j_k_ff_3 (
    .J(In[2]), .clk(and_1_out), .K(not_3_out), .Q(j_k_ff_3_q), .reset(Clr));  // open: Qn, preset, en
  not not_4 (not_4_out, In[3]);
  and and_5 (Output[3], Addr, j_k_ff_4_q);
  J_K_Flip_Flop j_k_ff_4 (
    .J(In[3]), .clk(and_1_out), .K(not_4_out), .Q(j_k_ff_4_q), .reset(Clr));  // open: Qn, preset, en
endmodule

// 2x4
module Memoria_2x4 (
  input  Addr,
  input  R_W,
  input  Clk,
  input  Clr,
  input  [3:0] Input,
  output [3:0] Output
);

  wire demultiplexer_1_out0, demultiplexer_1_out1;
  wire [3:0] memoria_1x4_1_output, memoria_1x4_2_output;

  Demultiplexer #(.enable("false")) demultiplexer_1 (
    .out0(demultiplexer_1_out0), .out1(demultiplexer_1_out1), .in(1'b1), .sel(Addr));
  Memoria_1x4 memoria_1x4_1 (
    .Addr(demultiplexer_1_out0), .R_W(R_W), .In(Input), .Clr(Clr), .Output(memoria_1x4_1_output), .Clk(Clk));
  Memoria_1x4 memoria_1x4_2 (
    .Addr(demultiplexer_1_out1), .R_W(R_W), .In(Input), .Clr(Clr), .Output(memoria_1x4_2_output), .Clk(Clk));
  Multiplexer #(.width(4), .enable("false")) multiplexer_1 (
    .in0(memoria_1x4_1_output), .in1(memoria_1x4_2_output), .out(Output), .sel(Addr));
endmodule

// 1x8
module Memoria_1x8 (
  input  Addr,
  input  R_W,
  input  Clk,
  input  Clr,
  input  [7:0] Input,
  output [7:0] Output
);

  Memoria_1x4 memoria_1x4_1 (.Addr(Addr), .R_W(R_W), .In(Input[3:0]), .Clr(Clr), .Output(Output[3:0]), .Clk(Clk));
  Memoria_1x4 memoria_1x4_2 (.Addr(Addr), .R_W(R_W), .In(Input[7:4]), .Clr(Clr), .Output(Output[7:4]), .Clk(Clk));
endmodule

// 2x8
module Memoria_4x8 (
  input  [1:0] Addr,
  input  R_W,
  input  Clk,
  input  Clr,
  input  [7:0] in_5,
  output [7:0] out_6
);

  wire demultiplexer_1_out0, demultiplexer_1_out1, demultiplexer_1_out2, demultiplexer_1_out3;
  wire [7:0] memoria_1x8_1_output, memoria_1x8_2_output, memoria_1x8_3_output, memoria_1x8_4_output;

  Demultiplexer #(.select(2), .enable("false")) demultiplexer_1 (
    .out0(demultiplexer_1_out0), .out1(demultiplexer_1_out1), .out2(demultiplexer_1_out2),
    .out3(demultiplexer_1_out3), .in(1'b1), .sel(Addr));
  Memoria_1x8 memoria_1x8_1 (
    .Addr(demultiplexer_1_out0), .R_W(R_W), .Clk(Clk), .Clr(Clr), .Input(in_5), .Output(memoria_1x8_1_output));
  Memoria_1x8 memoria_1x8_2 (
    .Addr(demultiplexer_1_out1), .R_W(R_W), .Clk(Clk), .Clr(Clr), .Input(in_5), .Output(memoria_1x8_2_output));
  Memoria_1x8 memoria_1x8_3 (
    .Addr(demultiplexer_1_out2), .R_W(R_W), .Clk(Clk), .Clr(Clr), .Input(in_5), .Output(memoria_1x8_3_output));
  Memoria_1x8 memoria_1x8_4 (
    .Addr(demultiplexer_1_out3), .R_W(R_W), .Clk(Clk), .Clr(Clr), .Input(in_5), .Output(memoria_1x8_4_output));
  Multiplexer #(.select(2), .width(8), .enable("false")) multiplexer_1 (
    .in0(memoria_1x8_1_output), .in1(memoria_1x8_2_output), .in2(memoria_1x8_3_output),
    .in3(memoria_1x8_4_output), .out(out_6), .sel(Addr));
endmodule

// 8x8
module Memoria_8x8 (
  input  [2:0] Addr,
  input  R_W,
  input  Clk,
  input  Clr,
  input  [7:0] Input,
  output [7:0] Output
);

  wire [1:0] demultiplexer_1_out0, demultiplexer_1_out1;
  wire [7:0] memoria_4x8_1_out_6, memoria_4x8_2_out_6;

  Demultiplexer #(.width(2), .enable("false")) demultiplexer_1 (
    .out0(demultiplexer_1_out0), .out1(demultiplexer_1_out1), .in(Addr[1:0]), .sel(Addr[2]));
  Memoria_4x8 memoria_4x8_1 (
    .Addr(demultiplexer_1_out0), .R_W(R_W), .Clk(Clk), .Clr(Clr), .in_5(Input), .out_6(memoria_4x8_1_out_6));
  Memoria_4x8 memoria_4x8_2 (
    .Addr(demultiplexer_1_out1), .R_W(R_W), .Clk(Clk), .Clr(Clr), .in_5(Input), .out_6(memoria_4x8_2_out_6));
  Multiplexer #(.width(8), .enable("false")) multiplexer_1 (
    .in0(memoria_4x8_1_out_6), .in1(memoria_4x8_2_out_6), .out(Output), .sel(Addr[2]));
endmodule

// 1x16
module Memoria_1x16 (
  input  Addr,
  input  R_W,
  input  Clk,
  input  Clr,
  input  [15:0] Input,
  output [15:0] Output
);

  Memoria_1x8 memoria_1x8_1 (.Addr(Addr), .R_W(R_W), .Clk(Clk), .Clr(Clr), .Input(Input[7:0]), .Output(Output[7:0]));
  Memoria_1x8 memoria_1x8_2 (.Addr(Addr), .R_W(R_W), .Clk(Clk), .Clr(Clr), .Input(Input[15:8]), .Output(Output[15:8]));
endmodule
