// Logisim project Exemplo0016 (extra).circ as structural Verilog: 1 circuit, main circuit main
module main (
  input  x,
  input  y,
  input  w,
  input  z,
  input  a,
  input  b,
  input  c,
  input  d,
  output out_9
);

  wire s1_out, s2_out, s3_out, s4_out, s5_out, s6_out, s7_out, s8_out, s9_out, s10_out, s11_out, s12_out,
       s13_out, s14_out, s15_out, s16_out, s17_out, s18_out, s19_out, s20_out, s21_out;

  nand s1 (s1_out, x, x);
  nand s2 (s2_out, y, y);
  nand s3 (s3_out, w, w);
  nand s4 (s4_out, z, z);
  nand s5 (s5_out, a, a);
  nand s6 (s6_out, b, b);
  nand s7 (s7_out, c, c);
  nand s8 (s8_out, d, d);
  nand s9 (s9_out, s1_out, s2_out);
  nand s10 (s10_out, s3_out, s4_out);
  nand s11 (s11_out, s5_out, s6_out);
  nand s12 (s12_out, s7_out, s8_out);
  nand s13 (s13_out, s9_out, s9_out);
  nand s14 (s14_out, s10_out, s10_out);
  nand s15 (s15_out, s11_out, s11_out);
  nand s16 (s16_out, s12_out, s12_out);
  nand s19 (s19_out, s17_out, s17_out);
  nand s17 (s17_out, s13_out, s14_out);
  nand s18 (s18_out, s15_out, s16_out);
  nand s20 (s20_out, s18_out, s18_out);
  nand s21 (s21_out, s19_out, s20_out);
  nand s22 (out_9, s21_out, s21_out);

  // Notes on the sheet:
  //   Isabel Bicalho Amaro 451580
  //   [(x'.y').(w'.z')].[(a'.b').(c'.d')]
endmodule
