// Logisim project Projeto do Extra01.circ as structural Verilog: 1 circuit, main circuit Circuito para Extra 01
module Circuito_para_Extra_01 (
  input  [7:0] a__7_0,
  output s
);

  nor NOR (s, a__7_0[0], a__7_0[1], a__7_0[2], a__7_0[3], a__7_0[4], a__7_0[5], a__7_0[6], a__7_0[7]);

  // Notes on the sheet:
  //   Entrada: Um byte
  //   Matrícula: 448662
  //   Nome: Josemar Alves Caetano
  //   Saída: 1 quando todos os bytem forem iguais a zero
endmodule
