// Logisim project Projeto do Extra02.circ as structural Verilog: 1 circuit, main circuit Circuito para Extra 02
module Circuito_para_Extra_02 (
  input  [7:0] a__7_0,
  output s
);

  or OR (s, a__7_0[7], a__7_0[6], a__7_0[5], a__7_0[4], a__7_0[3], a__7_0[2], a__7_0[1], a__7_0[0]);

  // Notes on the sheet:
  //   Entrada: Um byte
  //   Matrícula: 448662
  //   Nome: Josemar Alves Caetano
  //   Saída: 1 quando um dos seus bits for igual a zero
endmodule
