// Logisim project Exemplo0001.circ as structural Verilog: 1 circuit, main circuit main
module main (
  input  a,
  output s
);

  buf buffer_1 (s, a);

  // Notes on the sheet:
  //   Guia01 - Ex0001
  //   Lucas Cardoso - 441694
  //   buffer
endmodule
