// Logisim project Exemplo0002.circ as structural Verilog: 1 circuit, main circuit main
module main (
  input  a,
  output s
);

  not not_1 (s, a);

  // Notes on the sheet:
  //   Guia01 - Ex0002
  //   Lucas Cardoso - 441694
  //   NOT
endmodule
