// Logisim project Exemplo0003.circ as structural Verilog: 1 circuit, main circuit main
module main (
  input  a,
  input  b,
  output s
);

  and and_1 (s, a, b);

  // Notes on the sheet:
  //   Guia01 - Ex0003
  //   Lucas Cardoso - 441694
  //   AND
endmodule
