// Logisim project Exemplo0004.circ as structural Verilog: 1 circuit, main circuit main
module main (
  input  a,
  input  b,
  output s
);

  or or_1 (s, a, b);

  // Notes on the sheet:
  //   Guia 01 - Ex0004
  //   Lucas Cardoso - 441694
  //   OR
endmodule
