// Logisim project Exemplo0005.circ as structural Verilog: 1 circuit, main circuit main
module main (
  input  p,
  input  in_2,
  input  in_3,
  input  q,
  input  in_5,
  input  in_6,
  input  in_7,
  input  in_8,
  input  [3:0] p_2,
  input  [3:0] q_2,
  output s,
  output s_2
);

  ExactlyOne xor_1 (.out(s), .in0(p), .in1(in_2), .in2(in_3), .in3(q), .in4(in_5), .in5(in_6), .in6(in_7), .in7(in_8));
  ExactlyOne xor_2 (
    .out(s_2), .in0(p_2[0]), .in1(p_2[1]), .in2(p_2[2]), .in3(p_2[3]), .in4(q_2[0]), .in5(q_2[1]),
    .in6(q_2[2]), .in7(q_2[3]));

  // Notes on the sheet:
  //   Ver. 01
  //   Ver. 02
  //   XOR
  //   XOR
  //   Guia 01 - Ex0005
  //   Lucas Cardoso - 441694
endmodule
