// Logisim project Exercicio0001.circ as structural Verilog: 1 circuit, main circuit main
module main (
  input  in_1,
  input  in_2,
  input  in_3,
  input  b,
  output s,
  output s_2
);

  wire AND_out;

  nand NAND (s, in_1, in_2);
  and AND (AND_out, in_3, b);
  not not_1 (s_2, AND_out);

  // Notes on the sheet:
  //   Ver. 01
  //   Ver. 02
  //   Guia 01 - Exercício0001
  //   Lucas Cardoso - 441694
  //   a
  //   b
  //   a
  //   NOT
endmodule
