// Logisim project Exercicio0003.circ as structural Verilog: 1 circuit, main circuit main
module main (
  input  a,
  input  b,
  input  a_2,
  input  b_2,
  output s,
  output s_2
);

  wire XOR_out;

  xnor XNOR (s, a, b);
  xor XOR (XOR_out, a_2, b_2);
  not not_1 (s_2, XOR_out);

  // Notes on the sheet:
  //   Ver. 01
  //   Ver. 02
  //   Guia 01 - Exercício0003
  //   Lucas Cardoso - 441694
  //   NOT
endmodule
