// Logisim project Exercicio0004.circ as structural Verilog: 1 circuit, main circuit main
module main (
  input  in_1,
  input  in_2,
  output s
);

  wire not_1_out, not_2_out;

  not not_1 (not_1_out, in_1);
  not not_2 (not_2_out, in_2);
  or OR (s, not_1_out, not_2_out);

  // Notes on the sheet:
  //   a
  //   b
  //   NOT
  //   NOT
  //   Guia 01 - Exercício0004
  //   Lucas Cardoso - 441694
endmodule
