// Logisim project Exercicio0005.circ as structural Verilog: 1 circuit, main circuit main
module main (
  input  a,
  input  b,
  output s
);

  wire not_1_out, not_2_out;

  not not_1 (not_1_out, a);
  not not_2 (not_2_out, b);
  and AND (s, not_1_out, not_2_out);

  // Notes on the sheet:
  //   NOT
  //   NOT
  //   Guia 01 - Exercício0005
  //   Lucas Cardoso - 441694
endmodule
