// Logisim project Exercicio0006.circ as structural Verilog: 1 circuit, main circuit main
module main (
  input  a,
  input  b,
  output out_3
);

  wire not_1_out, not_2_out, OR_2_out, OR_out;

  not not_1 (not_1_out, b);
  not not_2 (not_2_out, a);
  or OR (OR_out, a, not_1_out);
  or OR_2 (OR_2_out, b, not_2_out);
  and AND (out_3, OR_out, OR_2_out);

  // Notes on the sheet:
  //   Guia01 - Exercício0006
  //   Lucas Cardoso - 441694
  //   NOT
  //   NOT
  //   s
endmodule
