// Logisim project Exercicio0007.circ as structural Verilog: 1 circuit, main circuit main
module main (
  input  a,
  input  b,
  output s
);

  wire not_1_out, not_2_out, OR_2_out, OR_out;

  not not_1 (not_1_out, a);
  not not_2 (not_2_out, b);
  or OR (OR_out, a, b);
  or OR_2 (OR_2_out, not_1_out, not_2_out);
  and AND (s, OR_out, OR_2_out);

  // Notes on the sheet:
  //   NOT
  //   NOT
  //   Guia 01 - Exercício0007
  //   Lucas Cardoso - 441694
endmodule
