// Logisim project Exercicio0008.circ as structural Verilog: 1 circuit, main circuit main
module main (
  input  b,
  input  c,
  input  d,
  input  in_4,
  input  [3:0] in_5,
  output s,
  output s_2
);

  and AND (s, b, c, d, in_4);
  and AND_2 (s_2, in_5[0], in_5[1], in_5[2], in_5[3]);

  // Notes on the sheet:
  //   Ver. 01
  //   Ver. 02
  //   a
  //   a
  //   Guia 01 - Exercício0008
  //   Lucas Cardoso - 441694
endmodule
