// Logisim project Exercicio0009.circ as structural Verilog: 1 circuit, main circuit main
module main (
  input  a,
  input  b,
  input  c,
  input  d,
  output s
);

  wire AND_2_out, AND_out;

  and AND (AND_out, a, b);
  and AND_2 (AND_2_out, c, d);
  and AND_3 (s, AND_out, AND_2_out);

  // Notes on the sheet:
  //   Guia 01 - Exercício0009
  //   Lucas Cardoso - 441694
endmodule
