// Logisim project Exercicio0010.circ as structural Verilog: 1 circuit, main circuit main
module main (
  input  b,
  input  in_2,
  input  c,
  input  d,
  output s
);

  wire OR_2_out, OR_out;

  or OR (OR_out, b, in_2);
  or OR_2 (OR_2_out, c, d);
  or OR_3 (s, OR_out, OR_2_out);

  // Notes on the sheet:
  //   a
  //   Guia 01 - Exercício0010
  //   Lucas Cardoso - 441694
endmodule
