// Logisim project Exercicio0012.circ as structural Verilog: 1 circuit, main circuit main
module main (
  input  a,
  input  b,
  input  c,
  input  d,
  input  e,
  input  f,
  input  g,
  input  h,
  input  [7:0] in_9,
  output s,
  output s_2
);

  wire OR_2_out, OR_3_out, OR_4_out, OR_5_out, OR_6_out, OR_out;

  or OR (OR_out, a, b);
  or OR_2 (OR_2_out, c, d);
  or OR_3 (OR_3_out, e, f);
  or OR_4 (OR_4_out, g, h);
  or OR_5 (OR_5_out, OR_out, OR_2_out);
  or OR_6 (OR_6_out, OR_3_out, OR_4_out);
  or OR_7 (s, OR_5_out, OR_6_out);
  or OR_8 (s_2, in_9[0], in_9[1], in_9[2], in_9[3], in_9[4], in_9[5], in_9[6], in_9[7]);

  // Notes on the sheet:
  //   Ver. 01
  //   Ver. 02
  //   a
  //   Guia 01 - Exercício0012
  //   Lucas Cardoso - 441694
endmodule
