// Logisim project EXTRA-01.circ as structural Verilog: 1 circuit, main circuit main
module main (
  input  A,
  input  B,
  input  C,
  input  D,
  input  E,
  input  F,
  input  G,
  input  H,
  output S
);

  nor nor1 (S, H, G, F, E, D, C, B, A);

  // Notes on the sheet:
  //   Milton costa teles da silva - 002751
endmodule
