// Logisim project EXTRA02.circ as structural Verilog: 1 circuit, main circuit main
module main (
  input  A,
  input  B,
  input  C,
  input  D,
  input  E,
  input  F,
  input  G,
  input  H,
  output S
);

  or or1 (S, H, G, F, E, D, C, B, A);
endmodule
