// Logisim project Exemplo0016.circ as structural Verilog: 1 circuit, main circuit Questao 11
module Questao_11 (
  input  [7:0] in_1,
  output out_2
);

  nor nor_1 (out_2, in_1[0], in_1[1], in_1[2], in_1[3], in_1[4], in_1[5], in_1[6], in_1[7]);
endmodule
