// Logisim project Exemplo0017.circ as structural Verilog: 1 circuit, main circuit Questao 12
module Questao_12 (
  input  [7:0] in_1,
  output out_2
);

  or or_1 (out_2, in_1[0], in_1[1], in_1[2], in_1[3], in_1[4], in_1[5], in_1[6], in_1[7]);
endmodule
