// Logisim project Exercicio0006 - Complemento de 1.circ as structural Verilog: 1 circuit, main circuit Complemento de 1
module Complemento_de_1 (
  input  [7:0] in_1,
  output [7:0] out_2
);

  assign out_2 = ~in_1;  // NOT_Gate not_1, 8 bits wide

  // Notes on the sheet:
  //   Guia 02 - Exercicio0006 - Extras
  //   João Henrique - 392734
endmodule
