// Logisim project Extras_guia01.circ as structural Verilog: 3 circuits, main circuit Principal
module Principal (
  input  [7:0] a,
  input  [7:0] b,
  output out_3,
  output out_4
);

  Extra0001 Ex01 (.a(a), .s(out_3));
  Extra0002 Ex02 (.b(b), .s(out_4));

  // Notes on the sheet:
  //   Extra0001 - Ana Cristina - 427385
  //   Extra0002 - Ana Cristina - 427385
endmodule

module Extra0001 (
  input  [7:0] a,
  output s
);

  wire z0_out, z1_out, z2_out, z3_out, z4_out, z5_out;

  xnor z0 (z0_out, a[0], a[1]);
  xnor z1 (z1_out, a[2], a[3]);
  xnor z2 (z2_out, a[4], a[5]);
  xnor z3 (z3_out, a[6], a[7]);
  xnor z4 (z4_out, z0_out, z1_out);
  xnor z5 (z5_out, z2_out, z3_out);
  xnor u_s (s, z4_out, z5_out);
endmodule

module Extra0002 (
  input  [7:0] b,
  output s
);

  wire z0_out, z1_out, z2_out, z3_out, z4_out, z5_out;

  and z0 (z0_out, b[0], b[1]);
  and z1 (z1_out, b[2], b[3]);
  and z2 (z2_out, b[4], b[5]);
  and z3 (z3_out, b[6], b[7]);
  and z4 (z4_out, z0_out, z1_out);
  and z5 (z5_out, z2_out, z3_out);
  and u_s (s, z4_out, z5_out);
endmodule
