// Logisim project Circuitos2.circ as structural Verilog
// MS
module Meia_Somador (
  input  A,
  input  B,
  output S0,
  output Carry_out
);

  xor xor_1 (S0, A, B);
  and and_1 (Carry_out, A, B);

  // Notes on the sheet:
  //   Meia somador p/ 2 bits
endmodule

// SC
module Somador_completo_4_bits (
  input  D0,
  input  C0,
  input  B0,
  input  A0,
  input  D1,
  input  C1,
  input  B1,
  input  A1,
  output S0,
  output S1,
  output S2,
  output S3,
  output Carry_out
);

  wire meia_somador_1_carry_out, somador_completo_1_carry_out, somador_completo_2_carry_out;

  Meia_Somador meia_somador_1 (.A(A0), .B(A1), .S0(S0), .Carry_out(meia_somador_1_carry_out));
  Somador_completo somador_completo_1 (
    .A(B0), .B(B1), .Carry_in(meia_somador_1_carry_out), .S0(S1), .Carry_out(somador_completo_1_carry_out));
  Somador_completo somador_completo_2 (
    .A(C0), .B(C1), .Carry_in(somador_completo_1_carry_out), .S0(S2), .Carry_out(somador_completo_2_carry_out));
  Somador_completo somador_completo_3 (
    .A(D0), .B(D1), .Carry_in(somador_completo_2_carry_out), .S0(S3), .Carry_out(Carry_out));

  // Notes on the sheet:
  //   Somador completo p/ 4 bits
endmodule

// SC
module Somador_completo (
  input  A,
  input  B,
  input  Carry_in,
  output S0,
  output Carry_out
);

  wire and_1_out, and_2_out, xor_1_out;

  xor xor_1 (xor_1_out, A, B);
  and and_1 (and_1_out, B, A);
  xor xor_2 (S0, xor_1_out, Carry_in);
  and and_2 (and_2_out, Carry_in, xor_1_out);
  or or_1 (Carry_out, and_2_out, and_1_out);

  // Notes on the sheet:
  //   Somador completo p/ 2 bits
endmodule

// C1
module Complemento_de_1 (
  input  D0,
  input  C0,
  input  B0,
  input  A0,
  output S0,
  output S1,
  output S2,
  output S3
);

  not not_1 (S0, A0);
  not not_2 (S1, B0);
  not not_3 (S2, C0);
  not not_4 (S3, D0);

  // Notes on the sheet:
  //   Complemento de 1
  //   p/ 8 bits
endmodule

module Complemento_de_2 (
  input  D0,
  input  C0,
  input  B0,
  input  A0,
  output S0,
  output S1,
  output S2,
  output S3,
  output Carry_out
);

  wire complemento_de_1_1_s0, complemento_de_1_1_s1, complemento_de_1_1_s2, complemento_de_1_1_s3;

  Complemento_de_1 complemento_de_1_1 (
    .D0(D0), .C0(C0), .B0(B0), .A0(A0), .S0(complemento_de_1_1_s0), .S1(complemento_de_1_1_s1),
    .S2(complemento_de_1_1_s2), .S3(complemento_de_1_1_s3));
  Somador_completo_4_bits somador_completo_4_bits_1 (
    .D0(complemento_de_1_1_s3), .C0(complemento_de_1_1_s2), .B0(complemento_de_1_1_s1),
    .A0(complemento_de_1_1_s0), .D1(1'b0), .C1(1'b0), .B1(1'b0), .A1(1'b1), .S0(S0), .S1(S1), .S2(S2),
    .S3(S3), .Carry_out(Carry_out));

  // Notes on the sheet:
  //   Complemento de 2
  //   p/ 4 bits
endmodule
