// Logisim project Exercicio0006.circ as structural Verilog: 1 circuit, main circuit main
module main (
  input  [7:0] in_1,
  output [7:0] out_2
);

  assign out_2 = ~in_1;  // NOT_Gate not_1, 8 bits wide

  // Notes on the sheet:
  //   a
  //   Guia02 - Exercicio0006
  //   Lucas Cardoso - 441694
  //   NOT
  //   s
endmodule
