// Logisim project Exercicio0007.circ as structural Verilog: 1 circuit, main circuit main
module main (
  input  [7:0] in_1,
  output [7:0] out_2,
  output [7:0] out_3
);

  assign out_2 = ~in_1;  // NOT_Gate not_1, 8 bits wide
  assign out_3 = ~(out_2 | 8'h1);  // NOR_Gate nor_1, 8 bits wide

  // Notes on the sheet:
  //   a
  //   b
  //   Guia02 - Exercicio0007
  //   Lucas Cardoso - 441694
  //   NOT
  //   C1
  //   s
  //   C2
endmodule
