// Logisim project Projeto de circuito para Extra01.circ as structural Verilog: 1 circuit, main circuit Circuito para Extra01
module Circuito_para_Extra01 (
  input  [7:0] a
);

  wire [7:0] not_1_out;

  assign not_1_out = ~a;  // NOT_Gate not_1, 8 bits wide
  // Probe on not_1_out

  // Notes on the sheet:
  //   Entrada: byte qualquer
  //   Matrícula: 448662
  //   Saída: O complemento de 1 deste byte.
  //   Nome: Josemar Alves Caetano
endmodule
