// Logisim project Projeto de circuito para Extra02.circ as structural Verilog: 2 circuits, main circuit Circuito para Extra02
module Circuito_para_Extra02 (
  input  [7:0] a,
  output out_2,
  output [7:0] out_3,
  output out_4
);

  Complemento_de_2 complemento_de_2_1 (.in_1(a), .out_2(out_2), .out_4(out_4), .out_3(out_3));

  // Notes on the sheet:
  //   Entrada: byte qualquer
  //   Overflow
  //   Valor adicional agregado à saída
  //   Matrícula: 448662
  //   Saída: O complemento de 2 deste byte.
  //   Nome: Josemar Alves Caetano
endmodule

module Complemento_de_2 (
  input  [7:0] in_1,
  output out_2,
  output [7:0] out_3,
  output out_4
);

  wire [7:0] bit_extender_1_out, not_1_out;

  assign bit_extender_1_out = {{7{1'b0}}, 1'b1};  // Bit_Extender bit_extender_1
  assign not_1_out = ~in_1;  // NOT_Gate not_1, 8 bits wide
  Adder adder_1 (.a(not_1_out), .b(bit_extender_1_out), .out(out_3), .cin(out_2), .cout(out_4));
endmodule
