// Logisim project Exercicio Extra 1 - Complemento 1.circ as structural Verilog: 1 circuit, main circuit Complemento de um de 1 Byte
module Complemento_de_um_de_1_Byte (
  input  [7:0] in_1,
  output [7:0] out_2
);

  assign out_2 = ~in_1;  // NOT_Gate not_1, 8 bits wide

  // Notes on the sheet:
  //   Matricula 449517
  //    Guia 02 - Exercicio Extra  1  - Complemento de 1
  //   Ana Carolina Conceição de Jesus
endmodule
