// Logisim project Exercicio Extra 2 - Complemento 2.circ as structural Verilog: 1 circuit, main circuit main
module main (
  input  in_1,
  input  [7:0] in_2,
  input  [7:0] in_3,
  input  in_4,
  output [7:0] out_5,
  output [7:0] out_6
);

  wire adder_1_cout;

  assign out_6 = ~in_3;  // NOT_Gate not_1, 8 bits wide
  Adder adder_1 (.a(in_2), .b(out_6), .out(out_5), .cin(in_1), .cout(adder_1_cout));

  // Notes on the sheet:
  //   Guia 02 - Exercicio Extra 2  - Complemento 2
  //   Ana Carolina Conceição de Jesus
  //   Matricula : 449517
endmodule
