// Logisim project Exemplo0032.circ as structural Verilog: 1 circuit, main circuit main
module main (
  input  A,
  input  B,
  input  CH__0_OR_1_AND,
  output S
);

  wire and0_out, and1_out, and2_out, not_1_out, or0_out;

  and and0 (and0_out, B, A);
  or or0 (or0_out, A, B);
  and and1 (and1_out, and0_out, CH__0_OR_1_AND);
  and and2 (and2_out, or0_out, not_1_out);
  not not_1 (not_1_out, CH__0_OR_1_AND);
  or or1 (S, and1_out, and2_out);

  // Notes on the sheet:
  //   Milton costa teles da silva - 002751
  //   s1
  //   s2
  //   s3
  //   s4
endmodule
