// Logisim project Exemplo0033.circ as structural Verilog: 1 circuit, main circuit main
module main (
  input  _0_nor_or__1_nand_and,
  input  A,
  input  B,
  input  _0_AND_OR_1_NAND_NOR,
  output s0
);

  wire and0_out, and1_out, and2_out, and3_out, and4_out, nand1_out, nor1_out, not_1_out, not_2_out,
       not_3_out, not_4_out, or1_out;

  nand nand1 (nand1_out, A, B);
  nor nor1 (nor1_out, A, B);
  and and0 (and0_out, A, B);
  or or1 (or1_out, A, B);
  and and1 (and1_out, _0_nor_or__1_nand_and, nand1_out, _0_AND_OR_1_NAND_NOR);
  not not_1 (not_1_out, _0_nor_or__1_nand_and);
  and and2 (and2_out, not_1_out, nor1_out, _0_AND_OR_1_NAND_NOR);
  and and3 (and3_out, _0_nor_or__1_nand_and, and0_out, not_2_out);
  not not_2 (not_2_out, _0_AND_OR_1_NAND_NOR);
  not not_3 (not_3_out, _0_nor_or__1_nand_and);
  and and4 (and4_out, not_3_out, or1_out, not_4_out);
  not not_4 (not_4_out, _0_AND_OR_1_NAND_NOR);
  or or2 (s0, and1_out, and2_out, and3_out, and4_out);

  // Notes on the sheet:
  //   Milton costa teles da silva-002751
  //   chave
  //   flag
  //   selecionavel
endmodule
