// Logisim project Exemplo0034.circ as structural Verilog: 1 circuit, main circuit main
module main (
  input  A,
  input  B,
  input  [1:0] _00_OR__01_NOR_10_XOR__11_XNOR,
  output S1
);

  wire AND1_out, AND2_out, AND3_out, AND4_out, NOR_out, not_1_out, not_2_out, not_3_out, not_4_out, OR0_out,
       xnor_out, xor_out;

  xor \xor  (xor_out, A, B);
  xnor \xnor  (xnor_out, A, B);
  or OR0 (OR0_out, A, B);
  nor NOR (NOR_out, A, B);
  not not_1 (not_1_out, _00_OR__01_NOR_10_XOR__11_XNOR[0]);
  not not_2 (not_2_out, _00_OR__01_NOR_10_XOR__11_XNOR[0]);
  not not_3 (not_3_out, _00_OR__01_NOR_10_XOR__11_XNOR[1]);
  not not_4 (not_4_out, _00_OR__01_NOR_10_XOR__11_XNOR[1]);
  and AND1 (AND1_out, not_1_out, xor_out, _00_OR__01_NOR_10_XOR__11_XNOR[1]);
  and AND2 (AND2_out, _00_OR__01_NOR_10_XOR__11_XNOR[1], _00_OR__01_NOR_10_XOR__11_XNOR[0], xnor_out);
  and AND3 (AND3_out, not_2_out, not_3_out, OR0_out);
  and AND4 (AND4_out, _00_OR__01_NOR_10_XOR__11_XNOR[0], not_4_out, NOR_out);
  or OR1 (S1, AND1_out, AND2_out, AND3_out, AND4_out);

  // Notes on the sheet:
  //   Milton costa teles da silva - 002751
endmodule
