// Logisim project Exemplo0035.circ as structural Verilog: 1 circuit, main circuit main
module main (
  input  A,
  input  B,
  input  [2:0] _000_NOT1,
  output S0
);

  wire AND0_out, AND1_out, AND2_out, AND3_out, AND4_out, AND5_out, AND6_out, AND7_out, AND8_out, NAND_out,
       NOR_out, NOT1_out, NOT2_out, not_1_out, not_2_out, not_3_out, not_4_out, not_5_out, not_6_out,
       not_7_out, not_8_out, not_9_out, not_10_out, not_11_out, not_12_out, OR0_out, XNOR_out, XOR_out;

  not NOT1 (NOT1_out, A);
  not NOT2 (NOT2_out, B);
  or OR0 (OR0_out, A, B);
  nor NOR (NOR_out, A, B);
  and AND0 (AND0_out, A, B);
  nand NAND (NAND_out, A, B);
  xor XOR (XOR_out, A, B);
  xnor XNOR (XNOR_out, A, B);
  not not_1 (not_1_out, _000_NOT1[2]);
  not not_2 (not_2_out, _000_NOT1[1]);
  not not_3 (not_3_out, _000_NOT1[0]);
  not not_4 (not_4_out, _000_NOT1[1]);
  not not_5 (not_5_out, _000_NOT1[2]);
  not not_6 (not_6_out, _000_NOT1[0]);
  not not_7 (not_7_out, _000_NOT1[2]);
  not not_8 (not_8_out, _000_NOT1[1]);
  not not_9 (not_9_out, _000_NOT1[0]);
  not not_10 (not_10_out, _000_NOT1[2]);
  not not_11 (not_11_out, _000_NOT1[1]);
  not not_12 (not_12_out, _000_NOT1[0]);
  and AND1 (AND1_out, not_1_out, not_2_out, not_3_out, NOT1_out);
  and AND2 (AND2_out, not_4_out, NOT2_out, not_5_out, _000_NOT1[0]);
  and AND3 (AND3_out, not_6_out, _000_NOT1[1], OR0_out, not_7_out);
  and AND4 (AND4_out, not_8_out, not_9_out, _000_NOT1[2], NOR_out);
  and AND5 (AND5_out, not_10_out, _000_NOT1[1], _000_NOT1[0], AND0_out);
  and AND6 (AND6_out, _000_NOT1[2], _000_NOT1[0], not_11_out, NAND_out);
  and AND7 (AND7_out, not_12_out, _000_NOT1[2], _000_NOT1[1], XOR_out);
  and AND8 (AND8_out, _000_NOT1[2], _000_NOT1[1], _000_NOT1[0], XNOR_out);
  or OR1 (S0, AND1_out, AND2_out, AND3_out, AND4_out, AND5_out, AND6_out, AND7_out, AND8_out);

  // Notes on the sheet:
  //   001-NOT2
  //   010-OR
  //   100-NOR
  //   011-AND
  //   101-NAND
  //   011-XOR
  //   111XNOR
endmodule
