// Logisim project exemplo0032.circ as structural Verilog: 1 circuit, main circuit main
module main (
  input  in_1,
  input  in_2,
  input  chave,
  output out_4,
  output out_5,
  output out_6
);

  wire and_2_out, and_3_out, not_1_out;

  and and_1 (out_4, in_1, in_2);
  or or_1 (out_6, in_1, in_2);
  not not_1 (not_1_out, chave);
  and and_2 (and_2_out, out_4, chave);
  and and_3 (and_3_out, out_6, not_1_out);
  or or_2 (out_5, and_2_out, and_3_out);

  // Notes on the sheet:
  //   0 = OR
  //   1 = AND
  //   Lucas Siqueira Chagas - 380783
  //   exercicio 02
endmodule
