// Logisim project exemplo0033.circ as structural Verilog: 1 circuit, main circuit main
module main (
  input  in_1,
  input  in_2,
  input  chave,
  output out_4,
  output AND___NAND,
  output out_6,
  output out_7,
  output OR___NOR,
  output out_9
);

  wire and_2_out, and_3_out, and_4_out, and_5_out, not_1_out, not_2_out;

  and and_1 (out_4, in_1, in_2);
  or or_1 (out_6, in_1, in_2);
  nand nand_1 (out_7, in_1, in_2);
  nor nor_1 (out_9, in_1, in_2);
  and and_2 (and_2_out, out_4, not_1_out);
  not not_1 (not_1_out, chave);
  and and_3 (and_3_out, out_7, chave);
  and and_4 (and_4_out, out_6, not_2_out);
  not not_2 (not_2_out, chave);
  and and_5 (and_5_out, out_9, chave);
  or or_2 (AND___NAND, and_2_out, and_3_out);
  or or_3 (OR___NOR, and_4_out, and_5_out);

  // Notes on the sheet:
  //   Lucas Siqueira Chagas - 380783
  //   exercicio 03
  //   0 = OR / AND
  //   1 = NOR/NAND
endmodule
