// Logisim project exemplo0036.circ as structural Verilog: 1 circuit, main circuit main
module main (
  input  in_1,
  input  in_2,
  input  in_3,
  input  in_4,
  input  in_5,
  output out_6,
  output out_7
);

  wire or_1_out, xor_1_out, xor_2_out;

  xor xor_1 (xor_1_out, in_1, in_3);
  xor xor_2 (xor_2_out, in_2, in_4);
  or or_1 (or_1_out, xor_1_out, xor_2_out);
  not not_1 (out_6, or_1_out);
  xor xor_3 (out_7, out_6, in_5);

  // Notes on the sheet:
  //   Lucas Siqueira Chagas - 380783
  //   exercicio 06
endmodule
