// Logisim project exemplo0037.circ as structural Verilog: 1 circuit, main circuit main
module main (
  input  in_1,
  input  in_2,
  input  in_3,
  input  in_4,
  input  _1_para_maior,
  output out_6,
  output se_maior_ascende,
  output saida_final,
  output out_9,
  output out_10,
  output out_11,
  output out_12
);

  wire and_3_out, not_1_out, xnor_1_out;

  xor xor_1 (out_10, in_1, in_3);
  xor xor_2 (out_12, in_2, in_4);
  or or_1 (out_6, out_12, out_10);
  and and_1 (out_9, in_1, out_10);
  not not_1 (not_1_out, out_10);
  and and_2 (out_11, in_2, out_12);
  or or_2 (se_maior_ascende, out_9, and_3_out);
  and and_3 (and_3_out, not_1_out, out_11);
  xnor xnor_1 (xnor_1_out, se_maior_ascende, _1_para_maior);
  and and_4 (saida_final, out_6, xnor_1_out);

  // Notes on the sheet:
  //   exercicio 07
  //   Lucas Siqueira Chagas - 380783
  //   0 para menor
  //   se diferente ascende
endmodule
