// Logisim project Exemplo0031.circ as structural Verilog: 1 circuit, main circuit main
module main (
  input  [3:0] in_1,
  input  [3:0] in_2
);

  wire [3:0] and_1_out, or_1_out, or_2_out;

  assign and_1_out = in_1 & in_2;  // AND_Gate and_1, 4 bits wide
  assign or_1_out = in_1 | in_2;  // OR_Gate or_1, 4 bits wide
  // Probe on or_2_out
  assign or_2_out = and_1_out | or_1_out;  // OR_Gate or_2, 4 bits wide
endmodule
