// Logisim project Exemplo0033.circ as structural Verilog: 1 circuit, main circuit main
module main (
  input  a,
  input  b,
  input  chave,
  output sAND_OR,
  output sNAND_NOR
);

  wire and_1_out, and_2_out, and_3_out, and_4_out, and_5_out, nand_1_out, nor_1_out, not_1_out, not_2_out,
       or_1_out;

  and and_1 (and_1_out, b, a);
  or or_1 (or_1_out, b, a);
  nand nand_1 (nand_1_out, b, a);
  nor nor_1 (nor_1_out, b, a);
  not not_1 (not_1_out, chave);
  not not_2 (not_2_out, chave);
  and and_2 (and_2_out, and_1_out, not_1_out);
  and and_3 (and_3_out, or_1_out, not_2_out);
  and and_4 (and_4_out, nand_1_out, chave);
  and and_5 (and_5_out, nor_1_out, chave);
  or or_2 (sAND_OR, and_2_out, and_3_out);
  or or_3 (sNAND_NOR, and_4_out, and_5_out);
endmodule
