// Logisim project Exemplo0037.circ as structural Verilog: 1 circuit, main circuit main
module main (
  input  a,
  input  b,
  input  chave,
  output s0,
  output s1
);

  wire and_1_out, and_2_out, not_1_out, not_2_out, not_3_out;

  not not_1 (not_1_out, a);
  not not_2 (not_2_out, b);
  and and_1 (and_1_out, not_1_out, b);
  and and_2 (and_2_out, a, not_2_out);
  and and_3 (s0, and_1_out, not_3_out);
  not not_3 (not_3_out, chave);
  and and_4 (s1, and_2_out, chave);

  // Notes on the sheet:
  //   s0 -> Menor (chave = 0)
  //   s1 -> Maior (chave = 1)
endmodule
