// Logisim project Circ Exemplo0035.circ as structural Verilog: 1 circuit, main circuit main
module main (
  input  [2:0] in_1,
  input  in_2,
  input  in_3,
  output out_4
);

  wire and_1_out, and_2_out, and_3_out, and_4_out, and_5_out, and_6_out, and_7_out, and_8_out, and_9_out,
       nand_1_out, nor_1_out, not_1_out, not_2_out, not_3_out, not_4_out, not_5_out, not_6_out, not_7_out,
       not_8_out, not_9_out, not_10_out, not_11_out, not_12_out, not_13_out, not_14_out, or_1_out,
       xnor_1_out, xor_1_out;

  xor xor_1 (xor_1_out, in_3, in_2);
  or or_1 (or_1_out, in_3, in_2);
  and and_1 (and_1_out, in_3, in_2);
  not not_1 (not_1_out, in_2);
  not not_2 (not_2_out, in_3);
  xnor xnor_1 (xnor_1_out, in_3, in_2);
  nor nor_1 (nor_1_out, in_3, in_2);
  nand nand_1 (nand_1_out, in_3, in_2);
  not not_3 (not_3_out, in_1[0]);
  not not_4 (not_4_out, in_1[1]);
  not not_5 (not_5_out, in_1[2]);
  not not_6 (not_6_out, in_1[1]);
  not not_7 (not_7_out, in_1[2]);
  not not_8 (not_8_out, in_1[0]);
  not not_9 (not_9_out, in_1[2]);
  not not_10 (not_10_out, in_1[2]);
  not not_11 (not_11_out, in_1[0]);
  not not_12 (not_12_out, in_1[1]);
  not not_13 (not_13_out, in_1[0]);
  not not_14 (not_14_out, in_1[0]);
  and and_2 (and_2_out, xor_1_out, not_3_out, not_4_out, not_5_out);
  and and_3 (and_3_out, or_1_out, in_1[0], not_6_out, not_7_out);
  and and_4 (and_4_out, and_1_out, not_8_out, in_1[1], not_9_out);
  and and_5 (and_5_out, xnor_1_out, in_1[0], in_1[1], not_10_out);
  and and_6 (and_6_out, nor_1_out, not_11_out, not_12_out, in_1[2]);
  and and_7 (and_7_out, nand_1_out, in_1[0], not_13_out, in_1[2]);
  and and_8 (and_8_out, not_1_out, not_14_out, in_1[1], in_1[2]);
  and and_9 (and_9_out, not_2_out, in_1[0], in_1[1], in_1[2]);
  or or_2 (out_4, and_2_out, and_3_out, and_4_out, and_5_out, and_6_out, and_7_out, and_8_out, and_9_out);

  // Notes on the sheet:
  //   Selecionador de bits(0 entra direita, 1 meio, 2 esquerda)
endmodule
