// Logisim project exemplo0032.circ as structural Verilog: 1 circuit, main circuit main
module main (
  input  in_1,
  input  in_2,
  input  in_3
);

  wire not_1_out;

  not not_1 (not_1_out, in_3);
  // AND_Gate and_1 has open pins: in0=in_2, in1=not_1_out, in2=in_1, out=open
  // OR_Gate or_1 has open pins: in0=in_2, in1=in_3, in2=in_1, out=open
endmodule
