// Logisim project Exemplo0031.circ as structural Verilog: 1 circuit, main circuit main
module main (
  input  [3:0] a,
  input  [3:0] b,
  output [3:0] s,
  output [3:0] s1
);

  assign s = a & b;  // AND_Gate and_1, 4 bits wide
  assign s1 = a | b;  // OR_Gate or_1, 4 bits wide

  // Notes on the sheet:
  //   Felipe Torres - 412738
endmodule
