// Logisim project Exemplo0033.circ as structural Verilog: 1 circuit, main circuit main
module main (
  input  A,
  input  B,
  input  in_3,
  output [1:0] out_4
);

  wire and_1_out, nand_1_out, nor_1_out, not_1_out, not_2_out, or_1_out;
  wire [1:0] and_2_out, and_4_out;

  nand nand_1 (nand_1_out, B, A);
  nor nor_1 (nor_1_out, B, A);
  and and_1 (and_1_out, B, A);
  or or_1 (or_1_out, B, A);
  not not_1 (not_1_out, in_3);
  and and_2 (and_2_out[0], nand_1_out, not_1_out);
  and and_3 (and_2_out[1], nor_1_out, not_2_out);
  not not_2 (not_2_out, in_3);
  and and_4 (and_4_out[0], in_3, or_1_out);
  and and_5 (and_4_out[1], in_3, and_1_out);
  assign out_4 = and_2_out | and_4_out;  // OR_Gate or_2, 2 bits wide

  // Notes on the sheet:
  //   Felipe Torres - 412738
endmodule
