// Logisim project Exemplo0035.circ as structural Verilog: 1 circuit, main circuit main
module main (
  input  a,
  input  b,
  input  chave,
  input  chave2,
  input  chave3,
  output out_6
);

  wire AND1_out, AND2_out, AND3_out, AND4_out, AND5_out, AND6_out, AND7_out, AND8_out, NAND1_out, NOR_out,
       not_1_out, not_2_out, not_3_out, not_4_out, not_5_out, not_6_out, not_7_out, not_8_out, not_9_out,
       not_10_out, not_11_out, not_12_out, not_13_out, OR1_out, XNOR1_out, XOR1_out;

  not not_1 (not_1_out, a);
  or OR1 (OR1_out, a, b);
  nor NOR (NOR_out, a, b);
  and AND1 (AND1_out, a, b);
  nand NAND1 (NAND1_out, a, b);
  xor XOR1 (XOR1_out, a, b);
  xnor XNOR1 (XNOR1_out, a, b);
  not not_2 (not_2_out, chave);
  not not_3 (not_3_out, chave2);
  not not_4 (not_4_out, chave3);
  not not_5 (not_5_out, chave);
  not not_6 (not_6_out, chave2);
  not not_7 (not_7_out, chave);
  not not_8 (not_8_out, chave3);
  not not_9 (not_9_out, chave);
  not not_10 (not_10_out, chave2);
  not not_11 (not_11_out, chave3);
  not not_12 (not_12_out, chave2);
  not not_13 (not_13_out, chave3);
  and AND2 (AND2_out, not_2_out, not_3_out, not_4_out, not_1_out);
  and AND3 (AND3_out, not_5_out, not_6_out, chave3, OR1_out);
  and AND4 (AND4_out, not_7_out, chave2, not_8_out, NOR_out);
  and AND5 (AND5_out, not_9_out, chave2, chave3, AND1_out);
  and AND6 (AND6_out, chave, not_10_out, not_11_out, NAND1_out);
  and AND7 (AND7_out, chave, not_12_out, chave3, XOR1_out);
  and AND8 (AND8_out, chave, chave2, not_13_out, XNOR1_out);
  or OR2 (out_6, AND2_out, AND3_out, AND4_out, AND5_out, AND6_out, AND7_out, AND8_out);

  // Notes on the sheet:
  //   Felipe Torres  - 412738
endmodule
