// Logisim project Exemplo0034.circ as structural Verilog: 1 circuit, main circuit main
module main (
  input  in_1,
  input  in_2,
  input  in_3,
  input  in_4,
  output out_5,
  output out_6,
  output out_7,
  output out_8,
  output out_9
);

  wire and_1_out, and_2_out, and_3_out, and_4_out, and_5_out, and_6_out, not_1_out, not_2_out, not_3_out,
       or_2_out, or_3_out;

  or or_1 (out_5, in_2, in_1);
  xor xor_1 (out_6, in_2, in_1);
  nor nor_1 (out_8, in_2, in_1);
  xnor xnor_1 (out_9, in_2, in_1);
  not not_1 (not_1_out, in_3);
  not not_2 (not_2_out, in_3);
  and and_1 (and_1_out, out_5, not_1_out);
  and and_2 (and_2_out, out_6, in_3);
  and and_3 (and_3_out, out_8, not_2_out);
  and and_4 (and_4_out, out_9, in_3);
  or or_2 (or_2_out, and_1_out, and_2_out);
  or or_3 (or_3_out, and_3_out, and_4_out);
  not not_3 (not_3_out, in_4);
  and and_5 (and_5_out, or_2_out, not_3_out);
  and and_6 (and_6_out, or_3_out, in_4);
  or or_4 (out_7, and_5_out, and_6_out);

  // Notes on the sheet:
  //   Guia 03 - Exemplo0034
  //   Fernando dos Santos Silva - 414506
endmodule
