// Logisim project Exemplo0035.circ as structural Verilog: 1 circuit, main circuit main
module main (
  input  in_1,
  input  in_2,
  input  in_3,
  input  in_4,
  input  in_5,
  output out_6,
  output out_7,
  output out_8,
  output out_9,
  output out_10,
  output out_11,
  output out_12,
  output out_13,
  output out_14
);

  wire and_2_out, and_3_out, and_4_out, and_5_out, and_6_out, and_7_out, and_8_out, and_9_out, and_10_out,
       and_11_out, and_12_out, and_13_out, and_14_out, and_15_out, not_3_out, not_4_out, not_5_out,
       not_6_out, not_7_out, not_8_out, not_9_out, or_2_out, or_3_out, or_4_out, or_5_out, or_6_out, or_7_out;

  not not_1 (out_6, in_2);
  not not_2 (out_7, in_1);
  and and_1 (out_8, in_2, in_1);
  or or_1 (out_9, in_2, in_1);
  nand nand_1 (out_11, in_2, in_1);
  nor nor_1 (out_12, in_2, in_1);
  xor xor_1 (out_13, in_2, in_1);
  xnor xnor_1 (out_14, in_2, in_1);
  and and_2 (and_2_out, out_6, not_3_out);
  not not_3 (not_3_out, in_3);
  and and_3 (and_3_out, out_7, in_3);
  and and_4 (and_4_out, out_8, not_4_out);
  not not_4 (not_4_out, in_3);
  and and_5 (and_5_out, out_9, in_3);
  and and_6 (and_6_out, out_11, not_5_out);
  not not_5 (not_5_out, in_3);
  and and_7 (and_7_out, out_12, in_3);
  and and_8 (and_8_out, out_13, not_6_out);
  not not_6 (not_6_out, in_3);
  and and_9 (and_9_out, out_14, in_3);
  or or_2 (or_2_out, and_2_out, and_3_out);
  or or_3 (or_3_out, and_4_out, and_5_out);
  or or_4 (or_4_out, and_6_out, and_7_out);
  or or_5 (or_5_out, and_8_out, and_9_out);
  not not_7 (not_7_out, in_4);
  not not_8 (not_8_out, in_4);
  and and_10 (and_10_out, or_2_out, not_7_out);
  and and_11 (and_11_out, or_3_out, in_4);
  and and_12 (and_12_out, or_4_out, not_8_out);
  and and_13 (and_13_out, or_5_out, in_4);
  or or_6 (or_6_out, and_10_out, and_11_out);
  or or_7 (or_7_out, and_12_out, and_13_out);
  not not_9 (not_9_out, in_5);
  and and_14 (and_14_out, or_6_out, not_9_out);
  and and_15 (and_15_out, or_7_out, in_5);
  or or_8 (out_10, and_14_out, and_15_out);

  // Notes on the sheet:
  //   000-NOT1;001-NAND;;010-AND;011-XOR;100-NOR;101-NOT2;110-OR;111-XNOR
  //   Guia 03 - Exemplo0035
  //   Fernando dos Santos Silva - 414506
endmodule
