// Logisim project Exemplo037.circ as structural Verilog: 1 circuit, main circuit main
module main (
  input  [1:0] in_1,
  input  [1:0] in_2,
  output out_3
);

  wire and_1_out, and_2_out, and_3_out, not_1_out, not_2_out, not_3_out;

  not not_1 (not_1_out, in_2[0]);
  not not_2 (not_2_out, in_2[0]);
  not not_3 (not_3_out, in_2[1]);
  and and_1 (and_1_out, in_1[0], not_1_out);
  and and_2 (and_2_out, in_1[1], not_2_out);
  and and_3 (and_3_out, in_1[1], not_3_out);
  or or_1 (out_3, and_1_out, and_2_out, and_3_out);
endmodule
