// Logisim project Exemplo0032.circ as structural Verilog: 2 circuits, main circuit Exemplo0032 - Ana Cristina
module Exemplo0032___Ana_Cristina (
  input  [1:0] a,
  input  [1:0] b,
  input  Flag,
  output [1:0] saida
);

  wire [1:0] AND_out, OR_out;

  assign AND_out = a & b;  // AND_Gate AND, 2 bits wide
  assign OR_out = a | b;  // OR_Gate OR, 2 bits wide
  Multiplexador Multiplexador (.\and (AND_out), .\or (OR_out), .chave(Flag), .saida(saida));

  // Notes on the sheet:
  //   0 - OR
  //   1 - AND
  //   Exemplo0032
endmodule

module Multiplexador (
  input  [1:0] \and ,
  input  [1:0] \or ,
  input  chave,
  output [1:0] saida
);

  wire [1:0] AND_2_out, AND_out, NOT_out;

  assign AND_out = \and  & {2{chave}};  // AND_Gate AND, 2 bits wide
  assign AND_2_out = \or  & NOT_out;  // AND_Gate AND_2, 2 bits wide
  assign NOT_out = ~{2{chave}};  // NOT_Gate NOT, 2 bits wide
  assign saida = AND_out | AND_2_out;  // OR_Gate OR, 2 bits wide
endmodule
