// Logisim project Exemplo0033.circ as structural Verilog: 2 circuits, main circuit Multiplexador
module Exemplo0033___Ana_Cristina (
  input  [1:0] a,
  input  [1:0] b,
  input  Flag,
  output [1:0] s,
  output [1:0] s1
);

  wire [1:0] AND_out, NAND_out, NOR_out, OR_out;

  assign AND_out = a & b;  // AND_Gate AND, 2 bits wide
  assign OR_out = a | b;  // OR_Gate OR, 2 bits wide
  assign NAND_out = ~(a & b);  // NAND_Gate NAND, 2 bits wide
  assign NOR_out = ~(a | b);  // NOR_Gate NOR, 2 bits wide
  Multiplexador multiplexador_1 (.a(AND_out), .b(OR_out), .Flag(Flag), .saida(s));
  Multiplexador multiplexador_2 (.a(NAND_out), .b(NOR_out), .Flag(Flag), .saida(s1));

  // Notes on the sheet:
  //   Exemplo0033
  //   0 - OR/AND
  //   1 - NOR/NAND
endmodule

module Multiplexador (
  input  [1:0] a,
  input  [1:0] b,
  input  Flag,
  output [1:0] saida
);

  wire [1:0] AND_2_out, AND_out, NOT_out;

  assign NOT_out = ~{2{Flag}};  // NOT_Gate NOT, 2 bits wide
  assign AND_out = a & {2{Flag}};  // AND_Gate AND, 2 bits wide
  assign AND_2_out = b & NOT_out;  // AND_Gate AND_2, 2 bits wide
  assign saida = AND_out | AND_2_out;  // OR_Gate OR, 2 bits wide
endmodule
