// Logisim project Exemplo0035.circ as structural Verilog: 2 circuits, main circuit Exemplo0035 - Ana Cristina
module Exemplo0035___Ana_Cristina (
  input  a,
  input  b,
  input  [2:0] Flag,
  output Saida
);

  wire and_1_out, nand_1_out, nor_1_out, not_1_out, not_2_out, or_1_out, xnor_1_out, xor_1_out;

  not not_1 (not_1_out, a);
  not not_2 (not_2_out, b);
  or or_1 (or_1_out, a, b);
  nor nor_1 (nor_1_out, a, b);
  and and_1 (and_1_out, a, b);
  nand nand_1 (nand_1_out, a, b);
  xor xor_1 (xor_1_out, a, b);
  xnor xnor_1 (xnor_1_out, a, b);
  Sel sel_1 (
    .a(not_1_out), .b(not_2_out), .c(or_1_out), .d(nor_1_out), .e(and_1_out), .f(nand_1_out), .g(xor_1_out),
    .h(xnor_1_out), .Flag(Flag), .Saida(Saida));

  // Notes on the sheet:
  //   Exemplo0035
  //   000 - NOT a
  //   001 - NOT b
  //   010 - OR
  //   011 - NOR
  //   100 - AND
  //   110 - XOR
  //   101 - NAND
  //   111 - XNOR
endmodule

// Selecionador
module Sel (
  input  a,
  input  b,
  input  c,
  input  d,
  input  e,
  input  f,
  input  g,
  input  h,
  input  [2:0] Flag,
  output Saida
);

  wire AND_2_out, AND_3_out, AND_4_out, AND_5_out, AND_6_out, AND_7_out, AND_8_out, AND_out, not_1_out,
       not_2_out, not_3_out, not_4_out, not_5_out, not_6_out, not_7_out, not_8_out, not_9_out, not_10_out,
       not_11_out, not_12_out;

  not not_1 (not_1_out, Flag[2]);
  not not_2 (not_2_out, Flag[1]);
  not not_3 (not_3_out, Flag[0]);
  not not_4 (not_4_out, Flag[2]);
  not not_5 (not_5_out, Flag[1]);
  not not_6 (not_6_out, Flag[2]);
  not not_7 (not_7_out, Flag[0]);
  not not_8 (not_8_out, Flag[2]);
  not not_9 (not_9_out, Flag[1]);
  not not_10 (not_10_out, Flag[0]);
  not not_11 (not_11_out, Flag[1]);
  not not_12 (not_12_out, Flag[0]);
  and AND (AND_out, a, not_1_out, not_2_out, not_3_out);
  and AND_2 (AND_2_out, b, not_4_out, not_5_out, Flag[0]);
  and AND_3 (AND_3_out, c, not_6_out, Flag[1], not_7_out);
  and AND_4 (AND_4_out, d, not_8_out, Flag[1], Flag[0]);
  and AND_5 (AND_5_out, e, Flag[2], not_9_out, not_10_out);
  and AND_6 (AND_6_out, f, Flag[2], not_11_out, Flag[0]);
  and AND_7 (AND_7_out, g, Flag[2], Flag[1], not_12_out);
  and AND_8 (AND_8_out, h, Flag[2], Flag[1], Flag[0]);
  or OR (Saida, AND_out, AND_2_out, AND_3_out, AND_4_out, AND_5_out, AND_6_out, AND_7_out, AND_8_out);
endmodule
