// Logisim project Exemplo0036.circ as structural Verilog: 2 circuits, main circuit Exemplo0036 - Ana Cristina
module Exemplo0036___Ana_Cristina (
  input  [3:0] x,
  input  [3:0] y,
  input  Flag,
  output [3:0] z
);

  wire [3:0] XNOR_out, XOR_out;

  assign XOR_out = y ^ x;  // XOR_Gate XOR, 4 bits wide
  assign XNOR_out = ~(y ^ x);  // XNOR_Gate XNOR, 4 bits wide
  Multiplexador multiplexador_1 (.a(XOR_out), .b(XNOR_out), .Flag(Flag), .saida(z));

  // Notes on the sheet:
  //   Exemplo0036
  //   0 - IGUALDADE
  //   1 - DIFERENÇA
endmodule

module Multiplexador (
  input  [3:0] a,
  input  [3:0] b,
  input  Flag,
  output [3:0] saida
);

  wire [3:0] AND_2_out, AND_out, NOT_out;

  assign AND_out = a & {4{Flag}};  // AND_Gate AND, 4 bits wide
  assign AND_2_out = b & NOT_out;  // AND_Gate AND_2, 4 bits wide
  assign NOT_out = ~{4{Flag}};  // NOT_Gate NOT, 4 bits wide
  assign saida = AND_out | AND_2_out;  // OR_Gate or_1, 4 bits wide
endmodule
