// Logisim project Exercicios.circ as structural Verilog
module Exercicio0031 (
  input  [3:0] A,
  input  [3:0] B,
  output [3:0] s_AND,
  output [3:0] s_OR
);

  assign s_AND = A & B;  // AND_Gate and_1, 4 bits wide
  assign s_OR = A | B;  // OR_Gate or_1, 4 bits wide
endmodule

module Exercicio0032 (
  input  chave,
  input  [1:0] AB,
  output s0
);

  wire and_1_out, and_2_out, and_3_out, not_1_out, or_1_out;

  and and_1 (and_1_out, AB[1], AB[0]);
  or or_1 (or_1_out, AB[0], AB[1]);
  and and_2 (and_2_out, chave, and_1_out);
  not not_1 (not_1_out, chave);
  and and_3 (and_3_out, not_1_out, or_1_out);
  or or_2 (s0, and_2_out, and_3_out);

  // Notes on the sheet:
  //   0 - OR
  //   1 - AND
endmodule

module Exercicio0033 (
  input  chave,
  input  [1:0] AB,
  output bit_1___OR___NOR,
  output out_4
);

  wire and_1_out, nand_1_out, nor_1_out, not_1_out, not_2_out, or_1_out;
  wire [1:0] and_2_out, and_4_out;

  and and_1 (and_1_out, AB[1], AB[0]);
  or or_1 (or_1_out, AB[0], AB[1]);
  nand nand_1 (nand_1_out, AB[0], AB[1]);
  nor nor_1 (nor_1_out, AB[0], AB[1]);
  not not_1 (not_1_out, chave);
  and and_2 (and_2_out[0], not_1_out, and_1_out);
  not not_2 (not_2_out, chave);
  and and_3 (and_2_out[1], not_2_out, or_1_out);
  and and_4 (and_4_out[0], chave, nand_1_out);
  and and_5 (and_4_out[1], chave, nor_1_out);
  assign {bit_1___OR___NOR, out_4} = and_2_out | and_4_out;  // OR_Gate or_2, 2 bits wide

  // Notes on the sheet:
  //   0 - OR - AND
  //   1 - NOR -NAND
  //   bit 0 - AND | NAND
endmodule

module Exercicio0034 (
  input  A,
  input  B,
  input  c1,
  input  c2,
  output S0
);

  wire and_1_out, and_2_out, and_3_out, and_4_out, NOR_out, not_1_out, not_2_out, not_3_out, not_4_out,
       OR_out, XNOR_out, XOR_out;

  xor XOR (XOR_out, B, A);
  xnor XNOR (XNOR_out, B, A);
  nor NOR (NOR_out, B, A);
  or OR (OR_out, B, A);
  not not_1 (not_1_out, c2);
  not not_2 (not_2_out, c1);
  not not_3 (not_3_out, c2);
  not not_4 (not_4_out, c1);
  and and_1 (and_1_out, not_1_out, c1, XOR_out);
  and and_2 (and_2_out, XNOR_out, c2, c1);
  and and_3 (and_3_out, NOR_out, c2, not_2_out);
  and and_4 (and_4_out, not_3_out, not_4_out, OR_out);
  or or_2 (S0, and_1_out, and_2_out, and_3_out, and_4_out);
endmodule

module Exercicio0035 (
  input  [1:0] AB,
  input  [2:0] chave,
  output out_3,
  output out_4
);

  wire and_1_out, and_2_out, nand_1_out, nor_1_out, or_1_out, xnor_1_out, xor_1_out;
  wire [1:0] not_1_out;

  assign {out_3, out_4} = and_2_out ? not_1_out : 2'bz;  // Controlled_Buffer buffer
  assign not_1_out = ~AB;  // NOT_Gate not_1, 2 bits wide
  or or_1 (or_1_out, AB[0], AB[1]);
  and and_1 (and_1_out, AB[0], AB[1]);
  and and_2 (and_2_out, ~chave[2], ~chave[1], ~chave[0]);  // AND_Gate
  nor nor_1 (nor_1_out, AB[0], AB[1]);
  nand nand_1 (nand_1_out, AB[0], AB[1]);
  xor xor_1 (xor_1_out, AB[0], AB[1]);
  xnor xnor_1 (xnor_1_out, AB[0], AB[1]);
  Multiplexer #(.select(3), .enable("false")) multiplexer_1 (
    .in1(or_1_out), .in2(nor_1_out), .in3(and_1_out), .in4(nand_1_out), .in5(xor_1_out), .in6(xnor_1_out),
    .out(out_4), .sel(chave));  // open: in0, in7

  // Notes on the sheet:
  //   000 - NOT
  //   001 - OR
  //   010 - NOR
  //   011 - AND
  //   100 - NAND
  //   101 - XOR 
  //   110 - XNOR
endmodule

module Exercicio0036 (
  input  a,
  input  b,
  input  chave,
  output s
);

  wire and_1_out, and_2_out, not_1_out, xnor_1_out, xor_1_out;

  not not_1 (not_1_out, a);
  xor xor_1 (xor_1_out, chave, b);
  and and_1 (and_1_out, xor_1_out, a);
  xnor xnor_1 (xnor_1_out, chave, b);
  and and_2 (and_2_out, xnor_1_out, not_1_out);
  or or_1 (s, and_1_out, and_2_out);

  // Notes on the sheet:
  //   chave 0 =  igual
  //   chave 1 = diferente
endmodule

module Exercicio0037 (
  input  a,
  input  b,
  input  chave,
  output s
);

  wire and_1_out, and_2_out;

  and and_1 (and_1_out, ~a, b, ~chave);  // AND_Gate
  and and_2 (and_2_out, chave, ~b, a);  // AND_Gate
  or or_1 (s, and_1_out, and_2_out);

  // Notes on the sheet:
  //   chave 0 = A < B
  //   chave 1 =  A > B
  //   valores iguais resultado = 0
endmodule
