// Logisim project Exemplo0031.circ as structural Verilog: 1 circuit, main circuit main
module main (
  input  [3:0] a,
  input  [3:0] b,
  output [3:0] S_b,
  output [3:0] S_a
);

  assign S_b = a & b;  // AND_Gate and_1, 4 bits wide
  assign S_a = a | b;  // OR_Gate or_1, 4 bits wide
endmodule
