// Logisim project Exemplo0032.circ as structural Verilog: 1 circuit, main circuit main
module main (
  input  in_1,
  input  in_2,
  input  in_3,
  input  in_4,
  input  in_5,
  input  in_6,
  output out_7,
  output out_8
);

  wire and_2_out, not_1_out, not_2_out, or_1_out, or_2_out, or_3_out, or_4_out, or_5_out;

  not not_1 (not_1_out, in_1);
  or or_1 (or_1_out, not_1_out, in_2);
  or or_2 (or_2_out, in_3, in_2);
  or or_3 (or_3_out, not_1_out, in_3);
  and and_1 (out_7, or_1_out, or_2_out, or_3_out);
  not not_2 (not_2_out, in_4);
  and and_2 (and_2_out, in_6, in_4, in_5);
  or or_4 (or_4_out, in_6, and_2_out, in_5);
  and and_3 (out_8, or_4_out, or_5_out);
  or or_5 (or_5_out, not_2_out, and_2_out);
endmodule
