// Logisim project Circuitos.circ as structural Verilog: 12 circuits, main circuit Exemplo0031
module Exemplo0031 (
  input  [3:0] Entrada,
  input  [3:0] Entrada_2,
  output [3:0] \Saída ,
  output [3:0] \Saída_2 
);

  assign \Saída  = Entrada_2 & Entrada;  // AND_Gate AND, 4 bits wide
  assign \Saída_2  = Entrada_2 | Entrada;  // OR_Gate OR, 4 bits wide

  // Notes on the sheet:
  //   Exemplo0031 - Djonatas Tulio Rodrigues Costa - 440954
endmodule

module Exemplo0032 (
  input  a,
  input  b,
  input  Chave,
  output s
);

  wire AND_A_out, AND_B_out, \AND_OR_saída , \AND_OR_saída_2 , not_1_out;

  andor AND_OR (.Entrada(a), .Entrada_2(b), .\Saída (\AND_OR_saída ), .\Saída_2 (\AND_OR_saída_2 ));
  not not_1 (not_1_out, Chave);
  and AND_A (AND_A_out, Chave, \AND_OR_saída );
  and AND_B (AND_B_out, \AND_OR_saída_2 , not_1_out);
  or OR (s, AND_A_out, AND_B_out);

  // Notes on the sheet:
  //   Exemplo0032 - Djonatas Tulio Rodrigues Costa - 440954
  //   0 - OR
  //   1 - AND
endmodule

module andor (
  input  Entrada,
  input  Entrada_2,
  output \Saída ,
  output \Saída_2 
);

  and AND (\Saída , Entrada_2, Entrada);
  or OR (\Saída_2 , Entrada_2, Entrada);

  // Notes on the sheet:
  //   Exemplo0031 - Djonatas Tulio Rodrigues Costa - 440954
endmodule

module Exemplo0033 (
  input  a,
  input  b,
  input  Chave,
  output Sa01,
  output Sa02
);

  wire and_1_out, and_2_out, and_3_out, and_4_out, \AND_OR_saída , \AND_OR_saída_2 , \NAND_NOR_saída ,
       \NAND_NOR_saída_2 , not_1_out, not_2_out;

  andor AND_OR (.Entrada(a), .Entrada_2(b), .\Saída (\AND_OR_saída ), .\Saída_2 (\AND_OR_saída_2 ));
  nandnor NAND_NOR (.Entrada(a), .Entrada_2(b), .\Saída (\NAND_NOR_saída ), .\Saída_2 (\NAND_NOR_saída_2 ));
  not not_1 (not_1_out, Chave);
  not not_2 (not_2_out, Chave);
  and and_1 (and_1_out, not_1_out, \AND_OR_saída );
  and and_2 (and_2_out, \AND_OR_saída_2 , not_2_out);
  and and_3 (and_3_out, Chave, \NAND_NOR_saída );
  and and_4 (and_4_out, \NAND_NOR_saída_2 , Chave);
  xor xor_1 (Sa01, and_1_out, and_3_out);
  xor xor_2 (Sa02, and_2_out, and_4_out);

  // Notes on the sheet:
  //   s1
  //   s2
  //   s3
  //   s4
  //   0 - AND-OR
  //   1 - NAND-NOR
  //   Exemplo0033 - Djonatas Tulio Rodrigues Costa - 440954
  //   s7
  //   s5
  //   s6
  //   s8
endmodule

module nandnor (
  input  Entrada,
  input  Entrada_2,
  output \Saída ,
  output \Saída_2 
);

  nand nand_1 (\Saída , Entrada_2, Entrada);
  nor nor_1 (\Saída_2 , Entrada_2, Entrada);

  // Notes on the sheet:
  //   Exemplo0031 - Djonatas Tulio Rodrigues Costa - 440954
endmodule

module Exemplo0034 (
  input  a,
  input  b,
  input  [1:0] Chave,
  output Sa01
);

  wire and_1_out, and_2_out, and_3_out, and_4_out, \OR_NOR_saída , \OR_NOR_saída_2 , \XOR_XNOR_saída ,
       \XOR_XNOR_saída_2 ;

  ornor OR_NOR (.Entrada(a), .Entrada_2(b), .\Saída (\OR_NOR_saída ), .\Saída_2 (\OR_NOR_saída_2 ));
  xorxnor XOR_XNOR (.Entrada(a), .Entrada_2(b), .\Saída (\XOR_XNOR_saída ), .\Saída_2 (\XOR_XNOR_saída_2 ));
  and and_1 (and_1_out, ~Chave[0], ~Chave[1], \OR_NOR_saída );  // AND_Gate
  and and_2 (and_2_out, \OR_NOR_saída_2 , ~Chave[1], Chave[0]);  // AND_Gate
  and and_3 (and_3_out, ~Chave[0], Chave[1], \XOR_XNOR_saída );  // AND_Gate
  and and_4 (and_4_out, \XOR_XNOR_saída_2 , Chave[1], Chave[0]);
  or or_1 (Sa01, and_1_out, and_2_out, and_3_out, and_4_out);

  // Notes on the sheet:
  //   00 - OR
  //   01 - NOR
  //   10 - XOR
  //   11 - XNOR
  //   Exemplo0034 - Djonatas Tulio Rodrigues Costa - 440954
  //   s1
  //   s2
  //   s3
  //   s4
  //   s5
  //   s6
  //   s7
  //   s8
endmodule

module ornor (
  input  Entrada,
  input  Entrada_2,
  output \Saída ,
  output \Saída_2 
);

  or OR (\Saída , Entrada_2, Entrada);
  nor NOR (\Saída_2 , Entrada_2, Entrada);

  // Notes on the sheet:
  //   Exemplo0031 - Djonatas Tulio Rodrigues Costa - 440954
endmodule

module xorxnor (
  input  Entrada,
  input  Entrada_2,
  output \Saída ,
  output \Saída_2 
);

  xor xor_1 (\Saída , Entrada_2, Entrada);
  xnor xnor_1 (\Saída_2 , Entrada_2, Entrada);

  // Notes on the sheet:
  //   Exemplo0031 - Djonatas Tulio Rodrigues Costa - 440954
endmodule

module Exemplo0035 (
  input  a,
  input  b,
  input  [2:0] in_3,
  output Sa01
);

  wire and_1_out, and_2_out, and_3_out, and_4_out, and_5_out, and_6_out, and_7_out, and_8_out,
       diversas_1_out_3, diversas_1_out_4, diversas_1_out_5, diversas_1_out_6, diversas_1_out_7,
       diversas_1_out_8, diversas_1_out_9, diversas_1_out_10;

  diversas diversas_1 (
    .in_1(a), .in_2(b), .out_3(diversas_1_out_3), .out_4(diversas_1_out_4), .out_5(diversas_1_out_5),
    .out_6(diversas_1_out_6), .out_7(diversas_1_out_7), .out_8(diversas_1_out_8), .out_9(diversas_1_out_9),
    .out_10(diversas_1_out_10));
  and and_1 (and_1_out, ~in_3[2], ~in_3[1], ~in_3[0], diversas_1_out_3);  // AND_Gate
  and and_2 (and_2_out, ~in_3[2], ~in_3[1], in_3[0], diversas_1_out_4);  // AND_Gate
  and and_3 (and_3_out, ~in_3[2], in_3[1], ~in_3[0], diversas_1_out_5);  // AND_Gate
  and and_4 (and_4_out, ~in_3[2], in_3[1], in_3[0], diversas_1_out_6);  // AND_Gate
  and and_5 (and_5_out, in_3[2], ~in_3[1], ~in_3[0], diversas_1_out_7);  // AND_Gate
  and and_6 (and_6_out, in_3[2], ~in_3[1], in_3[0], diversas_1_out_8);  // AND_Gate
  and and_7 (and_7_out, in_3[2], in_3[1], ~in_3[0], diversas_1_out_9);  // AND_Gate
  and and_8 (and_8_out, in_3[2], in_3[1], in_3[0], diversas_1_out_10);
  or or_1 (Sa01, and_1_out, and_2_out, and_3_out, and_4_out, and_5_out, and_6_out, and_7_out, and_8_out);

  // Notes on the sheet:
  //   s1
  //   s2
  //   s3
  //   s5
  //   s6
  //   s7
  //   s8
  //   000 - NOT(A)
  //   001 - NOT(B)
  //   010 - OR
  //   011 - NOR
  //   100 - AND
  //   101 - NAND
  //   110 - XOR
  //   111 - XNOR
  //   s4
  //   Exemplo0035 - Djonatas Tulio Rodrigues Costa - 440954
  //   p1
  //   p2
  //   p3
  //   p4
  //   p5
  //   p6
  //   p7
  //   p8
endmodule

// DIVERSAS
module diversas (
  input  in_1,
  input  in_2,
  output out_3,
  output out_4,
  output out_5,
  output out_6,
  output out_7,
  output out_8,
  output out_9,
  output out_10
);

  not not_1 (out_3, in_1);
  not not_2 (out_4, in_2);
  or or_1 (out_5, in_1, in_2);
  nor nor_1 (out_6, in_1, in_2);
  and and_1 (out_7, in_1, in_2);
  nand nand_1 (out_8, in_1, in_2);
  xor xor_1 (out_9, in_1, in_2);
  xnor xnor_1 (out_10, in_1, in_2);
endmodule

module Exemplo0036 (
  input  a,
  input  b,
  input  Chave,
  output Sa01
);

  wire and_1_out, and_2_out, XNOR_out, XOR_out;

  xor XOR (XOR_out, b, a);
  xnor XNOR (XNOR_out, b, a);
  and and_1 (and_1_out, Chave, XOR_out);
  and and_2 (and_2_out, XNOR_out, ~Chave);  // AND_Gate
  or or_1 (Sa01, and_1_out, and_2_out);

  // Notes on the sheet:
  //   Exemplo0036 - Djonatas Tulio Rodrigues Costa - 440954
endmodule

module Exemplo0037 (
  input  a,
  input  b,
  input  Chave,
  output out_4
);

  wire and_1_out, and_2_out, and_3_out, and_4_out, not_1_out, not_2_out;

  not not_1 (not_1_out, a);
  not not_2 (not_2_out, b);
  and and_1 (and_1_out, b, not_1_out);
  and and_2 (and_2_out, a, not_2_out);
  and and_3 (and_3_out, and_1_out, ~Chave);  // AND_Gate
  and and_4 (and_4_out, and_2_out, Chave);
  or or_1 (out_4, and_3_out, and_4_out);

  // Notes on the sheet:
  //   Exemplo0037 - Djonatas Tulio Rodrigues Costa - 440954
endmodule
