// Logisim project Exemplo0031.circ as structural Verilog: 2 circuits, main circuit main
module main (
  input  [3:0] in_1,
  input  [3:0] b,
  input  [3:0] in_3,
  input  [3:0] b_2,
  output [3:0] out_5,
  output [3:0] s1,
  output [3:0] out_7,
  output [3:0] out_8
);

  assign out_5 = in_1 & b;  // AND_Gate AND, 4 bits wide
  assign s1 = in_1 | b;  // OR_Gate OR, 4 bits wide
  LU LU (.in_1(in_3), .in_2(b_2), .out_3(out_7), .out_4(out_8));

  // Notes on the sheet:
  //   a
  //   a
  //   Guia03 - Exemplo0031
  //   Lucas Cardoso - 441694
  //   s
  //   s
  //   s1
endmodule

module LU (
  input  [3:0] in_1,
  input  [3:0] in_2,
  output [3:0] out_3,
  output [3:0] out_4
);

  assign out_3 = in_1 & in_2;  // AND_Gate and_1, 4 bits wide
  assign out_4 = in_1 | in_2;  // OR_Gate or_1, 4 bits wide
endmodule
