// Logisim project Exemplo0032.circ as structural Verilog: 2 circuits, main circuit main
module main (
  input  a,
  input  b,
  input  chave,
  output s
);

  wire AND_out, OR_out;

  and AND (AND_out, a, b);
  or OR (OR_out, a, b);
  LU lu_1 (.entrada1(AND_out), .entrada2(OR_out), .in_3(chave), .s(s));

  // Notes on the sheet:
  //   Guia03 - Exemplo0032
  //   Lucas Cardoso - 441694
  //   LU
  //   0 - OR
  //   1 - AND
endmodule

module LU (
  input  entrada1,
  input  entrada2,
  input  in_3,
  output s
);

  wire AND_2_out, AND_out, not_1_out;

  not not_1 (not_1_out, in_3);
  and AND (AND_out, entrada1, in_3);
  and AND_2 (AND_2_out, entrada2, not_1_out);
  or OR (s, AND_out, AND_2_out);

  // Notes on the sheet:
  //   NOT
  //   chave
endmodule
