// Logisim project Exemplo0033.circ as structural Verilog: 2 circuits, main circuit main
module main (
  input  a,
  input  b,
  input  chave,
  output s0,
  output s1
);

  wire AND_out, NAND_out, NOR_out, OR_out;

  and AND (AND_out, a, b);
  or OR (OR_out, a, b);
  nand NAND (NAND_out, a, b);
  nor NOR (NOR_out, a, b);
  LU LU (.b(AND_out), .c(OR_out), .d(NAND_out), .in_4(NOR_out), .chave(chave), .s0(s0), .s1(s1));

  // Notes on the sheet:
  //   Guia03 - Exemplo0033
  //   Lucas Cardoso - 441694
  //   0 - AND / OR
  //   1 - NAND / NOR
endmodule

module LU (
  input  b,
  input  c,
  input  d,
  input  in_4,
  input  chave,
  output s0,
  output s1
);

  wire AND1_out, AND2_out, AND3_out, AND4_out, not_1_out, not_2_out;

  not not_1 (not_1_out, chave);
  not not_2 (not_2_out, chave);
  and AND1 (AND1_out, b, not_1_out);
  and AND2 (AND2_out, c, not_2_out);
  and AND3 (AND3_out, d, chave);
  and AND4 (AND4_out, in_4, chave);
  or OR1 (s0, AND1_out, AND3_out);
  or OR2 (s1, AND2_out, AND4_out);

  // Notes on the sheet:
  //   a
  //   not
  //   not
endmodule
