// Logisim project Exemplo0034.circ as structural Verilog: 2 circuits, main circuit main
module main (
  input  in_1,
  input  in_2,
  input  [1:0] chave,
  output s
);

  wire NOR_out, OR_out, XNOR_out, XOR_out;

  or OR (OR_out, in_1, in_2);
  nor NOR (NOR_out, in_1, in_2);
  xor XOR (XOR_out, in_1, in_2);
  xnor XNOR (XNOR_out, in_1, in_2);
  LU LU (.b(OR_out), .c(NOR_out), .d(XOR_out), .in_4(XNOR_out), .in_5(chave), .s(s));

  // Notes on the sheet:
  //   Guia03 - Exemplo0034
  //   Lucas Cardoso - 441694
  //   00 - OR
  //   01 - NOR
  //   10 - XOR
  //   11 - XNOR
endmodule

module LU (
  input  b,
  input  c,
  input  d,
  input  in_4,
  input  [1:0] in_5,
  output s
);

  wire AND1_out, AND2_out, AND3_out, AND4_out, not_1_out, not_2_out, not_3_out, not_4_out;

  not not_1 (not_1_out, in_5[1]);
  not not_2 (not_2_out, in_5[0]);
  not not_3 (not_3_out, in_5[1]);
  not not_4 (not_4_out, in_5[0]);
  and AND1 (AND1_out, b, not_1_out, not_2_out);
  and AND2 (AND2_out, c, not_3_out, in_5[0]);
  and AND3 (AND3_out, d, in_5[1], not_4_out);
  and AND4 (AND4_out, in_4, in_5[1], in_5[0]);
  or OR (s, AND1_out, AND2_out, AND3_out, AND4_out);

  // Notes on the sheet:
  //   a
endmodule
