// Logisim project Exemplo0035.circ as structural Verilog: 2 circuits, main circuit main
module main (
  input  a,
  input  b,
  input  [2:0] chave,
  output s
);

  wire AND_out, NAND_out, NOR_out, NOT1_out, NOT2_out, OR_out, XNOR_out, XOR_out;

  not NOT1 (NOT1_out, a);
  not NOT2 (NOT2_out, b);
  or OR (OR_out, a, b);
  and AND (AND_out, a, b);
  nor NOR (NOR_out, a, b);
  nand NAND (NAND_out, a, b);
  xor XOR (XOR_out, a, b);
  xnor XNOR (XNOR_out, a, b);
  LU LU (
    .a(NOT1_out), .b(NOT2_out), .d(OR_out), .e(NOR_out), .f(AND_out), .g(NAND_out), .h(XOR_out),
    .in_8(XNOR_out), .in_9(chave), .s(s));

  // Notes on the sheet:
  //   000 - NOT A
  //   001 - NOT B
  //   010 - OR
  //   011 - NOR
  //   100 - AND
  //   101 - NAND
  //   110 - XOR
  //   111 - XNOR
  //   Guia03 - Exemplo0035
  //   Lucas Cardoso - 441694
endmodule

module LU (
  input  a,
  input  b,
  input  d,
  input  e,
  input  f,
  input  g,
  input  h,
  input  in_8,
  input  [2:0] in_9,
  output s
);

  wire AND1_out, AND2_out, AND3_out, AND4_out, AND5_out, AND6_out, AND7_out, AND8_out, not_1_out, not_2_out,
       not_3_out, not_4_out, not_5_out, not_6_out, not_7_out, not_8_out, not_9_out, not_10_out, not_11_out,
       not_12_out;

  not not_1 (not_1_out, in_9[2]);
  not not_2 (not_2_out, in_9[1]);
  not not_3 (not_3_out, in_9[0]);
  not not_4 (not_4_out, in_9[2]);
  not not_5 (not_5_out, in_9[1]);
  not not_6 (not_6_out, in_9[2]);
  not not_7 (not_7_out, in_9[0]);
  not not_8 (not_8_out, in_9[2]);
  not not_9 (not_9_out, in_9[1]);
  not not_10 (not_10_out, in_9[0]);
  not not_11 (not_11_out, in_9[1]);
  not not_12 (not_12_out, in_9[0]);
  and AND1 (AND1_out, a, not_1_out, not_2_out, not_3_out);
  and AND2 (AND2_out, b, not_4_out, not_5_out, in_9[0]);
  and AND3 (AND3_out, d, not_6_out, in_9[1], not_7_out);
  and AND4 (AND4_out, e, not_8_out, in_9[1], in_9[0]);
  and AND5 (AND5_out, f, in_9[2], not_9_out, not_10_out);
  and AND6 (AND6_out, g, in_9[2], not_11_out, in_9[0]);
  and AND7 (AND7_out, h, in_9[2], in_9[1], not_12_out);
  and AND8 (AND8_out, in_8, in_9[2], in_9[1], in_9[0]);
  or OR (s, AND1_out, AND2_out, AND3_out, AND4_out, AND5_out, AND6_out, AND7_out, AND8_out);

  // Notes on the sheet:
  //   c
endmodule
