// Logisim project Exemplo0031.circ as structural Verilog: 2 circuits, main circuit LU
module LU (
  input  [3:0] in_1,
  input  [3:0] in_2,
  output [3:0] out_3,
  output [3:0] out_4
);

  assign out_3 = in_1 & in_2;  // AND_Gate and_1, 4 bits wide
  assign out_4 = in_1 | in_2;  // OR_Gate or_1, 4 bits wide
endmodule

module Exemplo31 (
  input  [3:0] in_1,
  input  [3:0] in_2,
  input  [3:0] OR___1111,
  output [3:0] out_4
);

  wire [3:0] and_1_out, and_2_out, lu_1_out_3, lu_1_out_4, not_1_out;

  LU lu_1 (.in_1(in_1), .in_2(in_2), .out_3(lu_1_out_3), .out_4(lu_1_out_4));
  assign not_1_out = ~OR___1111;  // NOT_Gate not_1, 4 bits wide
  assign and_1_out = not_1_out & lu_1_out_3;  // AND_Gate and_1, 4 bits wide
  assign and_2_out = lu_1_out_4 & OR___1111;  // AND_Gate and_2, 4 bits wide
  assign out_4 = and_1_out | and_2_out;  // OR_Gate or_1, 4 bits wide

  // Notes on the sheet:
  //   AND - 0000
endmodule
