// Logisim project Exemplo0033.circ as structural Verilog: 3 circuits, main circuit andor
module andor (
  input  in_1,
  input  in_2,
  output out_3,
  output out_4
);

  and and_1 (out_3, in_1, in_2);
  or or_1 (out_4, in_1, in_2);
endmodule

module Exemplo33 (
  input  OR___1,
  input  NAND_NOR___0,
  input  in_3,
  input  in_4,
  input  NAND___0,
  output out_6
);

  wire and_1_out, and_2_out, and_3_out, and_4_out, and_5_out, and_6_out, andor_1_out_3, andor_1_out_4,
       nandnor_1_out_3, nandnor_1_out_4, not_1_out, not_2_out, not_3_out, or_1_out, or_2_out;

  not not_1 (not_1_out, OR___1);
  andor andor_1 (.in_1(in_3), .in_2(in_4), .out_3(andor_1_out_3), .out_4(andor_1_out_4));
  nandnor nandnor_1 (.in_1(in_3), .in_2(in_4), .out_3(nandnor_1_out_3), .out_4(nandnor_1_out_4));
  not not_2 (not_2_out, NAND___0);
  and and_1 (and_1_out, not_1_out, andor_1_out_3);
  not not_3 (not_3_out, NAND_NOR___0);
  or or_1 (or_1_out, and_1_out, and_2_out);
  and and_2 (and_2_out, andor_1_out_4, OR___1);
  and and_3 (and_3_out, nandnor_1_out_3, not_2_out);
  or or_2 (or_2_out, and_3_out, and_4_out);
  and and_4 (and_4_out, nandnor_1_out_4, NAND___0);
  and and_5 (and_5_out, NAND_NOR___0, or_1_out);
  and and_6 (and_6_out, not_3_out, or_2_out);
  or or_3 (out_6, and_5_out, and_6_out);

  // Notes on the sheet:
  //   AND - 0
  //   NOR - 1
  //   AND/OR - 1
endmodule

module nandnor (
  input  in_1,
  input  in_2,
  output out_3,
  output out_4
);

  nand nand_1 (out_3, in_1, in_2);
  nor nor_1 (out_4, in_1, in_2);
endmodule
