// Logisim project Exemplo0034.circ as structural Verilog: 3 circuits, main circuit xorxnor
module xorxnor (
  input  in_1,
  input  in_2,
  output out_3,
  output out_4
);

  xor xor_1 (out_3, in_1, in_2);
  xnor xnor_1 (out_4, in_1, in_2);
endmodule

module Exemplo34 (
  input  in_1,
  input  in_2,
  input  [1:0] _00___XOR,
  output out_4
);

  wire and_1_out, and_2_out, and_3_out, and_4_out, not_1_out, not_2_out, ornor_1_out_3, ornor_1_out_4,
       xorxnor_1_out_3, xorxnor_1_out_4;

  not not_1 (not_1_out, _00___XOR[1]);
  not not_2 (not_2_out, _00___XOR[0]);
  xorxnor xorxnor_1 (.in_1(in_1), .in_2(in_2), .out_3(xorxnor_1_out_3), .out_4(xorxnor_1_out_4));
  ornor ornor_1 (.in_1(in_1), .in_2(in_2), .out_3(ornor_1_out_3), .out_4(ornor_1_out_4));
  and and_1 (and_1_out, xorxnor_1_out_3, not_1_out, not_2_out);
  and and_2 (and_2_out, xorxnor_1_out_4, _00___XOR[0], not_1_out);
  and and_3 (and_3_out, ornor_1_out_3, not_2_out, _00___XOR[1]);
  and and_4 (and_4_out, ornor_1_out_4, _00___XOR[1], _00___XOR[0]);
  or or_1 (out_4, and_1_out, and_2_out, and_3_out, and_4_out);

  // Notes on the sheet:
  //   10 - OR
  //   01 - XNOR
  //   11 - NOR
endmodule

module ornor (
  input  in_1,
  input  in_2,
  output out_3,
  output out_4
);

  or or_1 (out_3, in_1, in_2);
  nor nor_1 (out_4, in_1, in_2);
endmodule
