// Logisim project Exemplo0035.circ as structural Verilog: 2 circuits, main circuit LU
module LU (
  input  in_1,
  input  in_2,
  output out_3,
  output out_4,
  output out_5,
  output out_6,
  output out_7,
  output out_8,
  output out_9,
  output out_10
);

  not not_1 (out_3, in_1);
  not not_2 (out_4, in_2);
  or or_1 (out_5, in_1, in_2);
  nor nor_1 (out_6, in_1, in_2);
  and and_1 (out_7, in_1, in_2);
  nand nand_1 (out_8, in_1, in_2);
  xor xor_1 (out_9, in_1, in_2);
  xnor xnor_1 (out_10, in_1, in_2);
endmodule

module Exemplo35 (
  input  in_1,
  input  in_2,
  input  [2:0] in_3,
  output out_4
);

  wire and_1_out, and_2_out, and_3_out, and_4_out, and_5_out, and_6_out, and_7_out, and_8_out, lu_1_out_3,
       lu_1_out_4, lu_1_out_5, lu_1_out_6, lu_1_out_7, lu_1_out_8, lu_1_out_9, lu_1_out_10, not_1_out,
       not_2_out, not_3_out;

  LU lu_1 (
    .in_1(in_1), .in_2(in_2), .out_3(lu_1_out_3), .out_4(lu_1_out_4), .out_5(lu_1_out_5), .out_6(lu_1_out_6),
    .out_7(lu_1_out_7), .out_8(lu_1_out_8), .out_9(lu_1_out_9), .out_10(lu_1_out_10));
  not not_1 (not_1_out, in_3[2]);
  not not_2 (not_2_out, in_3[1]);
  not not_3 (not_3_out, in_3[0]);
  and and_1 (and_1_out, lu_1_out_3, in_3[2], in_3[1], in_3[0]);
  and and_2 (and_2_out, lu_1_out_4, in_3[2], in_3[1], not_3_out);
  and and_3 (and_3_out, in_3[0], lu_1_out_5, in_3[2], not_2_out, in_3[0]);
  and and_4 (and_4_out, lu_1_out_6, in_3[2], not_2_out, not_3_out);
  and and_5 (and_5_out, lu_1_out_7, not_1_out, in_3[1], in_3[0]);
  and and_6 (and_6_out, lu_1_out_8, not_1_out, in_3[1], not_3_out);
  and and_7 (and_7_out, lu_1_out_9, not_2_out, not_1_out, in_3[0]);
  and and_8 (and_8_out, lu_1_out_10, not_1_out, not_2_out, not_3_out);
  or or_1 (out_4, and_1_out, and_2_out, and_3_out, and_4_out, and_5_out, and_6_out, and_7_out, and_8_out);

  // Notes on the sheet:
  //   000 - XNOR
  //   001 - XOR
  //   010 - NAND
  //   011 - AND
  //   100 - NOR
  //   101 - OR
  //   110 - NOT B
  //   111 - NOT A
endmodule
