// Logisim project Exemplo0036.circ as structural Verilog: 2 circuits, main circuit LU
module LU (
  input  [1:0] in_1,
  input  [1:0] in_2,
  output [1:0] out_3,
  output [1:0] out_4
);

  assign out_3 = in_1 ^ in_2;  // XOR_Gate xor_1, 2 bits wide
  assign out_4 = ~(in_1 ^ in_2);  // XNOR_Gate xnor_1, 2 bits wide
endmodule

module Exemplo36 (
  input  [1:0] in_1,
  input  [1:0] in_2,
  input  [1:0] DIFERENCA___00,
  output [1:0] out_4
);

  wire [1:0] and_1_out, and_2_out, lu_1_out_3, lu_1_out_4, not_1_out;

  LU lu_1 (.in_1(in_1), .in_2(in_2), .out_3(lu_1_out_3), .out_4(lu_1_out_4));
  assign not_1_out = ~DIFERENCA___00;  // NOT_Gate not_1, 2 bits wide
  assign and_1_out = not_1_out & lu_1_out_3;  // AND_Gate and_1, 2 bits wide
  assign and_2_out = lu_1_out_4 & DIFERENCA___00;  // AND_Gate and_2, 2 bits wide
  assign out_4 = and_1_out | and_2_out;  // OR_Gate or_1, 2 bits wide

  // Notes on the sheet:
  //   IGUALDADE - 11
endmodule
