// Logisim project Exemplo0037.circ as structural Verilog: 2 circuits, main circuit main
module main (
  input  [1:0] in_1,
  input  [1:0] in_2,
  input  [1:0] _00__MAIOR,
  output [1:0] out_4
);

  wire [1:0] and_1_out, and_2_out, lu_1_out_3, lu_1_out_4, not_1_out;

  LU lu_1 (.in_1(in_1), .in_2(in_2), .out_3(lu_1_out_3), .out_4(lu_1_out_4));
  assign not_1_out = ~_00__MAIOR;  // NOT_Gate not_1, 2 bits wide
  assign and_1_out = not_1_out & lu_1_out_3;  // AND_Gate and_1, 2 bits wide
  assign and_2_out = lu_1_out_4 & _00__MAIOR;  // AND_Gate and_2, 2 bits wide
  assign out_4 = and_1_out | and_2_out;  // OR_Gate or_1, 2 bits wide

  // Notes on the sheet:
  //   11 - MENOR
endmodule

module LU (
  input  [1:0] in_1,
  input  [1:0] in_2,
  output [1:0] out_3,
  output [1:0] out_4
);

  wire [1:0] not_1_out, not_2_out;

  assign not_1_out = ~in_1;  // NOT_Gate not_1, 2 bits wide
  assign not_2_out = ~in_2;  // NOT_Gate not_2, 2 bits wide
  assign out_3 = in_1 & not_2_out;  // AND_Gate and_1, 2 bits wide
  assign out_4 = not_1_out & in_2;  // AND_Gate and_2, 2 bits wide
endmodule
