// Logisim project Circ Exemplo0034.circ as structural Verilog: 1 circuit, main circuit main
module main (
  input  [1:0] in_1,
  input  in_2,
  input  in_3,
  output s
);

  wire and1_out, and2_out, and3_out, and4_out, and5_out, and6_out, nor1_out, not_1_out, not_2_out, or1_out,
       or_1_out, or_2_out, xnor1_out, xor1_out;

  not not_1 (not_1_out, in_1[1]);
  xor xor1 (xor1_out, in_2, in_3);
  or or1 (or1_out, in_2, in_3);
  xnor xnor1 (xnor1_out, in_2, in_3);
  nor nor1 (nor1_out, in_2, in_3);
  and and1 (and1_out, in_1[1], xor1_out);
  and and2 (and2_out, not_1_out, or1_out);
  and and3 (and3_out, in_1[1], xnor1_out);
  and and4 (and4_out, not_1_out, nor1_out);
  not not_2 (not_2_out, in_1[0]);
  or or_1 (or_1_out, and1_out, and2_out);
  or or_2 (or_2_out, and3_out, and4_out);
  and and5 (and5_out, or_1_out, not_2_out);
  and and6 (and6_out, in_1[0], or_2_out);
  or or2 (s, and5_out, and6_out);

  // Notes on the sheet:
  //   s1
  //   s2
  //   s3
  //   s4
  //   s5
  //   s6
  //   s7
  //   s8
  //   s9
  //   s10
  //   CHAVE
  //   00 - OR
  //   01 - NOR
  //   10 - XOR
  //   11 XNOR
  //   s11
  //   s12
endmodule
