// Logisim project Projeto de circuito Exemplo0031.circ as structural Verilog: 2 circuits, main circuit Circuito Exemplo0031
module Circuito_Exemplo0031 (
  input  [3:0] a,
  input  [3:0] b,
  output [3:0] out_3,
  output [3:0] out_4
);

  LU_01 LU (.a(a), .b(b), .s0(out_3), .s1(out_4));

  // Notes on the sheet:
  //   Saída da OR
  //   Saída da AND
  //   Matrícula: 448662
  //   Nome: Josemar Alves Caetano
endmodule

module LU_01 (
  input  [3:0] a,
  input  [3:0] b,
  output [3:0] s0,
  output [3:0] s1
);

  assign s0 = a & b;  // AND_Gate AND_1, 4 bits wide
  assign s1 = b | a;  // OR_Gate OR_1, 4 bits wide

  // Notes on the sheet:
  //   Saída da AND
  //   Saída da OR
endmodule
