// Logisim project Projeto de circuito Exemplo0032.circ as structural Verilog: 2 circuits, main circuit Exemplo0032
module Exemplo0032 (
  input  a,
  input  b,
  input  chave,
  output S
);

  LU_02 LU_02 (.a(a), .b(b), .chave(chave), .S(S));

  // Notes on the sheet:
  //   Chaveamento: 0 - OR
  //   1 - AND
  //   Matrícula: 448662
  //   Nome: Josemar Alves Caetano
endmodule

module LU_02 (
  input  a,
  input  b,
  input  chave,
  output S
);

  wire AND_1_out, AND_2_out, AND_3_out, not_1_out, OR_1_out;

  and AND_1 (AND_1_out, b, a);
  or OR_1 (OR_1_out, b, a);
  not not_1 (not_1_out, chave);
  and AND_2 (AND_2_out, AND_1_out, chave);
  and AND_3 (AND_3_out, OR_1_out, not_1_out);
  or OR_2 (S, AND_2_out, AND_3_out);

  // Notes on the sheet:
  //   s0
  //   s1
  //   c0
  //   c1
  //   d0
  //   d1
endmodule
