// Logisim project Projeto de circuito Exemplo0033.circ as structural Verilog: 2 circuits, main circuit Exemplo0033
module Exemplo0033 (
  input  a,
  input  b,
  input  chave,
  output S0,
  output S1
);

  LU_03 LU_03 (.a(a), .b(b), .chave(chave), .S0(S0), .S1(S1));

  // Notes on the sheet:
  //   Chaveamento: 0 - OR e AND
  //   1 - NAND e NOR
  //   Saída AND
  //   Saída OR
  //   Saída NAND
  //   Saída NOR
  //   Matrícula: 448662
  //   Nome: Josemar Alves Caetano
endmodule

module LU_03 (
  input  a,
  input  b,
  input  chave,
  output S0,
  output S1
);

  wire AND1_out, AND2_out, AND3_out, AND4_out, AND5_out, NAND1_out, NOR1_out, not_1_out, OR_1_out;

  and AND1 (AND1_out, a, b);
  nand NAND1 (NAND1_out, b, a);
  or OR_1 (OR_1_out, b, a);
  nor NOR1 (NOR1_out, b, a);
  not not_1 (not_1_out, chave);
  and AND2 (AND2_out, AND1_out, not_1_out);
  and AND3 (AND3_out, NAND1_out, chave);
  and AND4 (AND4_out, OR_1_out, not_1_out);
  and AND5 (AND5_out, NOR1_out, chave);
  or OR_2 (S0, AND2_out, AND3_out);
  or OR_3 (S1, AND4_out, AND5_out);

  // Notes on the sheet:
  //   s0
  //   s1
  //   s2
  //   s3
  //   c0
  //   c1
  //   d0
  //   d1
  //   d2
  //   d3
  //   chave = 0
  //   Saída AND
  //   Saída OR
  //   Saída NAND
  //   Saída NOR
  //   chave = 1
endmodule
