// Logisim project Projeto de circuito Exemplo0034.circ as structural Verilog: 2 circuits, main circuit Exemplo0034
module Exemplo0034 (
  input  a,
  input  b,
  input  [1:0] in_3,
  output S
);

  LU_04 LU_04 (.a(a), .b(b), .in_3(in_3), .S(S));

  // Notes on the sheet:
  //   Chaveamento: 00 - OR
  //   01 - NOR
  //   10 - XOR
  //   11 - XNOR
  //   Matrícula: 448662
  //   Nome: Josemar Alves Caetano
endmodule

module LU_04 (
  input  a,
  input  b,
  input  [1:0] in_3,
  output S
);

  wire AND1_out, AND2_out, AND3_out, AND4_out, NOR_1_out, not_1_out, not_2_out, OR_1_out, XNOR_1_out,
       XOR_1_out;

  or OR_1 (OR_1_out, a, b);
  nor NOR_1 (NOR_1_out, a, b);
  xor XOR_1 (XOR_1_out, a, b);
  xnor XNOR_1 (XNOR_1_out, a, b);
  not not_1 (not_1_out, in_3[1]);
  not not_2 (not_2_out, in_3[0]);
  and AND1 (AND1_out, OR_1_out, not_1_out, not_2_out);
  and AND2 (AND2_out, NOR_1_out, not_1_out, in_3[0]);
  and AND3 (AND3_out, XOR_1_out, in_3[1], not_2_out);
  and AND4 (AND4_out, XNOR_1_out, in_3[1], in_3[0]);
  or OR_2 (S, AND1_out, AND2_out, AND3_out, AND4_out);

  // Notes on the sheet:
  //   Legenda:
  //   c[x]n - Chave na posição (0 ou 1) negada
  //   c[x]b - Chave na posição (0 ou 1) bufferizada
  //   s0
  //   s1
  //   s2
  //   s3
  //   c[1]n
  //   c[0]n
  //   c[1]n
  //   c[0]b
  //   c[1]b
  //   c[1]b
  //   Chaveamento: 00 - OR
  //   c[0]n
  //   c[0]b
  //   01 - NOR
  //   10 - XOR
  //   11 - XNOR
  //   d2
  //   d0
  //   d1
  //   d3
endmodule
