// Logisim project Projeto de circuito Exemplo0035.circ as structural Verilog: 2 circuits, main circuit Exemplo0035
module Exemplo0035 (
  input  a,
  input  b,
  input  [2:0] chave,
  output S
);

  LU_05 LU_05 (.a(a), .b(b), .chave(chave), .S(S));

  // Notes on the sheet:
  //   Chaveamento: 000 - NOT(a)
  //   001 - NOT(b)
  //   010 - OR
  //   011 - NOR
  //   100 - AND
  //   101 - NAND
  //   110 - XOR
  //   111 - XNOR
  //   Nome: Josemar Alves Caetano
  //   Matrícula: 448662
endmodule

module LU_05 (
  input  a,
  input  b,
  input  [2:0] chave,
  output S
);

  wire AND1_out, AND2_out, AND3_out, AND4_out, AND5_out, AND6_out, AND7_out, AND8_out, AND9_out, NAND1_out,
       NOR1_out, NOT1_out, NOT2_out, not_1_out, not_2_out, not_3_out, OR1_out, XNOR1_out, XOR1_out;

  not NOT1 (NOT1_out, a);
  not NOT2 (NOT2_out, b);
  or OR1 (OR1_out, a, b);
  nor NOR1 (NOR1_out, a, b);
  and AND1 (AND1_out, a, b);
  nand NAND1 (NAND1_out, a, b);
  xor XOR1 (XOR1_out, a, b);
  xnor XNOR1 (XNOR1_out, a, b);
  not not_1 (not_1_out, chave[2]);
  not not_2 (not_2_out, chave[0]);
  not not_3 (not_3_out, chave[1]);
  and AND2 (AND2_out, NOT1_out, not_1_out, not_3_out, not_2_out);
  and AND3 (AND3_out, NOT2_out, not_1_out, not_3_out, chave[0]);
  and AND4 (AND4_out, OR1_out, not_1_out, chave[1], not_2_out);
  and AND5 (AND5_out, NOR1_out, not_1_out, chave[1], chave[0]);
  and AND6 (AND6_out, AND1_out, chave[2], not_3_out, not_2_out);
  and AND7 (AND7_out, NAND1_out, chave[2], not_3_out, chave[0]);
  and AND8 (AND8_out, XOR1_out, chave[2], chave[1], not_2_out);
  and AND9 (AND9_out, XNOR1_out, chave[2], chave[1], chave[0]);
  or OR2 (S, AND2_out, AND3_out, AND4_out, AND5_out, AND6_out, AND7_out, AND8_out, AND9_out);

  // Notes on the sheet:
  //   Legenda:
  //   c[x]n - Chave na posição (0 ou 1) negada
  //   c[x]b - Chave na posição (0 ou 1) bufferizada
  //   s0
  //   s1
  //   s2
  //   s3
  //   s4
  //   s5
  //   s6
  //   s7
  //   c[2]b
  //   c[2]n
  //   c[1]b
  //   c[1]n
  //   c[0]n
  //   c[0]b
  //   d0
  //   d1
  //   d2
  //   d3
  //   d4
  //   d5
  //   d6
  //   d7
  //   Chaveamento: 000 - NOT(a)
  //   001 - NOT(b)
  //   010 - OR
  //   011 - NOR
  //   100 - AND
  //   101 - NAND
  //   110 - XOR
  //   111 - XNOR
endmodule
