// Logisim project Projeto de circuito Exemplo0036.circ as structural Verilog: 2 circuits, main circuit Exemplo0036
module Exemplo0036 (
  input  [1:0] a,
  input  [1:0] b,
  input  [1:0] chave,
  output [1:0] S
);

  LU_06 LU_06 (.a(a), .b(b), .chave(chave), .S(S));

  // Notes on the sheet:
  //   Chaveamento: 00 - Igual
  //   11 - Diferente
  //   Obs.: PROFESSOR, NÃO CONSEGUI USAR UMA CHAVE DE APENAS 1 BIT, TENTEI USAR A FERRAMENTA DISTRIBUIDOR, PORÉM SEM SUCESSO.
  //   Nome: Josemar Alves Caetano
  //   Matrícula: 448662
endmodule

module LU_06 (
  input  [1:0] a,
  input  [1:0] b,
  input  [1:0] chave,
  output [1:0] S
);

  wire [1:0] AND1_out, AND2_out, not_1_out, XNOR1_out, XOR1_out;

  assign XNOR1_out = ~(a ^ b);  // XNOR_Gate XNOR1, 2 bits wide
  assign XOR1_out = a ^ b;  // XOR_Gate XOR1, 2 bits wide
  assign not_1_out = ~chave;  // NOT_Gate not_1, 2 bits wide
  assign AND1_out = XNOR1_out & not_1_out;  // AND_Gate AND1, 2 bits wide
  assign AND2_out = XOR1_out & chave;  // AND_Gate AND2, 2 bits wide
  assign S = AND1_out | AND2_out;  // OR_Gate OR1, 2 bits wide

  // Notes on the sheet:
  //   s0
  //   s1
  //   c0
  //   c1
  //   d0
  //   d1
  //   Chaveamento: 00 - Igual
  //   11 - Diferente
endmodule
