// Logisim project Projeto de circuito Exemplo0037.circ as structural Verilog: 4 circuits, main circuit Exemplo0037
module Exemplo0037 (
  input  [1:0] a,
  input  [1:0] b,
  input  [1:0] chave,
  output [1:0] S
);

  LU_07 LU_07 (.a(a), .b(b), .chave(chave), .S(S));

  // Notes on the sheet:
  //   Chaveamento: 00 - Menor
  //   11 - Maior
  //   Obs.: PROFESSOR, NÃO CONSEGUI USAR UMA CHAVE DE APENAS 1 BIT, TENTEI USAR A FERRAMENTA DISTRIBUIDOR, PORÉM SEM SUCESSO.
  //   Matrícula: 448662
  //   Nome: Josemar Alves Caetano
endmodule

module LU_07 (
  input  [1:0] a,
  input  [1:0] b,
  input  [1:0] chave,
  output [1:0] S
);

  wire [1:0] AND3_out, AND4_out, Maior_s0, Menor_s1, not_1_out;

  Maior Maior (.a(a), .b(b), .S0(Maior_s0));
  Menor Menor (.a(a), .b(b), .S1(Menor_s1));
  assign not_1_out = ~chave;  // NOT_Gate not_1, 2 bits wide
  assign AND3_out = Maior_s0 & chave;  // AND_Gate AND3, 2 bits wide
  assign AND4_out = Menor_s1 & not_1_out;  // AND_Gate AND4, 2 bits wide
  assign S = AND3_out | AND4_out;  // OR_Gate OR1, 2 bits wide

  // Notes on the sheet:
  //   s1
  //   s0
  //   c0
  //   c1
  //   Chaveamento: 00 - Menor
  //   d0
  //   d1
  //   11 - Maior
endmodule

module Maior (
  input  [1:0] a,
  input  [1:0] b,
  output [1:0] S0
);

  wire [1:0] not_1_out;

  assign not_1_out = ~b;  // NOT_Gate not_1, 2 bits wide
  assign S0 = a & not_1_out;  // AND_Gate AND1, 2 bits wide
endmodule

module Menor (
  input  [1:0] a,
  input  [1:0] b,
  output [1:0] S1
);

  wire [1:0] not_1_out;

  assign not_1_out = ~a;  // NOT_Gate not_1, 2 bits wide
  assign S1 = not_1_out & b;  // AND_Gate AND2, 2 bits wide
endmodule
