// Logisim project exemplo_0031.circ as structural Verilog: 2 circuits, main circuit main
module main (
  input  [3:0] in_1,
  input  [3:0] in_2,
  output [3:0] out_3,
  output [3:0] out_4
);

  assign out_3 = in_1 & in_2;  // AND_Gate and_1, 4 bits wide
  assign out_4 = in_1 | in_2;  // OR_Gate or_1, 4 bits wide
endmodule

module LU_4 (
  input  [3:0] in_1,
  input  [3:0] in_2,
  input  [3:0] in_3,
  output [3:0] out_4
);

  wire [3:0] and_1_out, and_2_out, and_or_out_3, and_or_out_4, not_1_out;

  main and_or (.in_1(in_1), .in_2(in_2), .out_3(and_or_out_3), .out_4(and_or_out_4));
  assign not_1_out = ~in_3;  // NOT_Gate not_1, 4 bits wide
  assign and_1_out = not_1_out & and_or_out_3;  // AND_Gate and_1, 4 bits wide
  assign and_2_out = and_or_out_4 & in_3;  // AND_Gate and_2, 4 bits wide
  assign out_4 = and_1_out | and_2_out;  // OR_Gate or_1, 4 bits wide

  // Notes on the sheet:
  //   Exerecicio0031
  //   Átila Martins Silva Júnior - 449014
  //   LU AND OR 4b
  //   0000_AND
  //   1111_OR
endmodule
