// Logisim project exemplos_0032_0033.circ as structural Verilog: 5 circuits, main circuit main
module main (
  input  in_1,
  input  in_2,
  output out_3,
  output out_4
);

  and and_1 (out_3, in_1, in_2);
  or or_1 (out_4, in_1, in_2);
endmodule

module LU_and_or_1b (
  input  in_1,
  input  in_2,
  input  _0_AND,
  output out_4
);

  wire and_1_out, and_2_out, main_1_out_3, main_1_out_4, not_1_out;

  main main_1 (.in_1(in_1), .in_2(in_2), .out_3(main_1_out_3), .out_4(main_1_out_4));
  not not_1 (not_1_out, _0_AND);
  and and_1 (and_1_out, not_1_out, main_1_out_3);
  and and_2 (and_2_out, main_1_out_4, _0_AND);
  or or_1 (out_4, and_1_out, and_2_out);

  // Notes on the sheet:
  //   Exercicio_ 0032
  //   Átila Martins Silva Júnior - 449014
  //   and/or
  //   1_OR
endmodule

module nand_nor (
  input  in_1,
  input  in_2,
  output out_3,
  output out_4
);

  nand nand_1 (out_3, in_1, in_2);
  nor nor_1 (out_4, in_1, in_2);
endmodule

module LU_and_or_nand_nor (
  input  _1_NOR,
  input  in_2,
  input  in_3,
  input  _0_AND,
  input  _0_NAND_NOR,
  output out_6
);

  wire and_1_out, and_2_out, lu_and_or_1b_1_out_4, lu_nand_nor_1_out_4, not_1_out;

  LU_nand_nor lu_nand_nor_1 (.in_2(in_2), .in_3(in_3), ._1_NOR(_1_NOR), .out_4(lu_nand_nor_1_out_4));
  LU_and_or_1b lu_and_or_1b_1 (.in_1(in_3), .in_2(in_2), ._0_AND(_0_AND), .out_4(lu_and_or_1b_1_out_4));
  not not_1 (not_1_out, _0_NAND_NOR);
  and and_1 (and_1_out, lu_nand_nor_1_out_4, not_1_out);
  and and_2 (and_2_out, lu_and_or_1b_1_out_4, _0_NAND_NOR);
  or or_1 (out_6, and_1_out, and_2_out);

  // Notes on the sheet:
  //   Exercicio0033
  //   Átila Martins Silva Júnior - 449014
  //   1_OR
  //   0_NAND
  //   1_AND/OR
endmodule

module LU_nand_nor (
  input  _1_NOR,
  input  in_2,
  input  in_3,
  output out_4
);

  wire and_1_out, and_2_out, nand_nor_1_out_3, nand_nor_1_out_4, not_1_out;

  nand_nor nand_nor_1 (.in_1(in_2), .in_2(in_3), .out_3(nand_nor_1_out_3), .out_4(nand_nor_1_out_4));
  not not_1 (not_1_out, _1_NOR);
  and and_1 (and_1_out, not_1_out, nand_nor_1_out_3);
  and and_2 (and_2_out, nand_nor_1_out_4, _1_NOR);
  or or_1 (out_4, and_1_out, and_2_out);

  // Notes on the sheet:
  //   0_NAND
endmodule
