// Logisim project circuitos.circ as structural Verilog: 10 circuits, main circuit main
module main (
  input  [3:0] in_1,
  input  [3:0] in_2,
  output [3:0] out_3,
  output [3:0] out_4
);

  assign out_3 = in_1 & in_2;  // AND_Gate and_1, 4 bits wide
  assign out_4 = in_1 | in_2;  // OR_Gate or_1, 4 bits wide
endmodule

module exemplo031 (
  input  [3:0] in_1,
  input  [3:0] in_2,
  output [3:0] out_3,
  output [3:0] out_4
);

  assign out_3 = in_1 & in_2;  // AND_Gate and_1, 4 bits wide
  assign out_4 = in_1 | in_2;  // OR_Gate or_1, 4 bits wide

  // Notes on the sheet:
  //   guilherme alves de oliveira - mat 450161
endmodule

module andeor (
  input  in_1,
  input  in_2,
  output out_3,
  output out_4
);

  and and_1 (out_3, in_1, in_2);
  or or_1 (out_4, in_1, in_2);
endmodule

module exemplo032 (
  input  in_1,
  input  in_2,
  input  in_3,
  output out_4
);

  wire and_1_out, and_2_out, andeor_1_out_3, andeor_1_out_4, not_1_out;

  andeor andeor_1 (.in_1(in_1), .in_2(in_2), .out_3(andeor_1_out_3), .out_4(andeor_1_out_4));
  and and_1 (and_1_out, andeor_1_out_3, in_3);
  not not_1 (not_1_out, in_3);
  and and_2 (and_2_out, not_1_out, andeor_1_out_4);
  or or_1 (out_4, and_1_out, and_2_out);

  // Notes on the sheet:
  //   guilherme alvbes de oliveira
endmodule

module xor_xnor (
  input  in_1,
  input  in_2,
  output out_3,
  output out_4
);

  xor xor_1 (out_3, in_1, in_2);
  xnor xnor_1 (out_4, in_1, in_2);
endmodule

module or_nor (
  input  in_1,
  input  in_2,
  output out_3,
  output out_4
);

  or or_1 (out_3, in_1, in_2);
  nor nor_1 (out_4, in_2, in_1);
endmodule

module exemplo034 (
  input  in_1,
  input  in_2,
  input  [1:0] in_3,
  output out_4
);

  wire and_1_out, and_2_out, and_3_out, and_4_out, not_1_out, not_2_out, not_3_out, not_4_out,
       or_nor_1_out_3, or_nor_1_out_4, xor_xnor_1_out_3, xor_xnor_1_out_4;

  or_nor or_nor_1 (.in_1(in_2), .in_2(in_1), .out_3(or_nor_1_out_3), .out_4(or_nor_1_out_4));
  xor_xnor xor_xnor_1 (.in_1(in_1), .in_2(in_2), .out_3(xor_xnor_1_out_3), .out_4(xor_xnor_1_out_4));
  not not_1 (not_1_out, in_3[0]);
  not not_2 (not_2_out, in_3[1]);
  not not_3 (not_3_out, in_3[1]);
  not not_4 (not_4_out, in_3[0]);
  and and_1 (and_1_out, xor_xnor_1_out_4, in_3[0], in_3[1]);
  and and_2 (and_2_out, not_1_out, not_2_out, or_nor_1_out_3);
  and and_3 (and_3_out, or_nor_1_out_4, not_3_out, in_3[0]);
  and and_4 (and_4_out, xor_xnor_1_out_3, not_4_out, in_3[1]);
  or or_1 (out_4, and_2_out, and_1_out, and_3_out, and_4_out);

  // Notes on the sheet:
  //   00  - or
  //   01 - Nor
  //   10 - xor
  //   11 - xnor
endmodule

module exemplo035 (
  input  in_1,
  input  in_2,
  input  [2:0] in_3,
  output out_4
);

  wire and_1_out, and_2_out, and_3_out, and_4_out, and_5_out, and_6_out, and_7_out, and_8_out, and_9_out,
       nand_1_out, nor_1_out, not_1_out, not_2_out, not_3_out, not_4_out, not_5_out, not_6_out, not_7_out,
       not_8_out, not_9_out, not_10_out, not_11_out, not_12_out, not_13_out, not_14_out, or_1_out,
       xnor_1_out, xor_1_out;

  not not_1 (not_1_out, in_1);
  not not_2 (not_2_out, in_2);
  or or_1 (or_1_out, in_1, in_2);
  nor nor_1 (nor_1_out, in_1, in_2);
  and and_1 (and_1_out, in_1, in_2);
  nand nand_1 (nand_1_out, in_2, in_2, in_1);
  xor xor_1 (xor_1_out, in_2, in_1);
  xnor xnor_1 (xnor_1_out, in_2, in_1);
  not not_3 (not_3_out, in_3[0]);
  not not_4 (not_4_out, in_3[1]);
  not not_5 (not_5_out, in_3[2]);
  not not_6 (not_6_out, in_3[1]);
  not not_7 (not_7_out, in_3[2]);
  not not_8 (not_8_out, in_3[0]);
  not not_9 (not_9_out, in_3[2]);
  not not_10 (not_10_out, in_3[2]);
  not not_11 (not_11_out, in_3[0]);
  not not_12 (not_12_out, in_3[1]);
  not not_13 (not_13_out, in_3[1]);
  not not_14 (not_14_out, in_3[0]);
  and and_2 (and_2_out, not_1_out, not_3_out, not_4_out, not_5_out);
  and and_3 (and_3_out, not_6_out, not_7_out, not_2_out, in_3[0]);
  and and_4 (and_4_out, not_8_out, or_1_out, in_3[1], not_9_out);
  and and_5 (and_5_out, in_3[0], nor_1_out, in_3[1], not_10_out);
  and and_6 (and_6_out, in_3[2], and_1_out, not_11_out, not_12_out);
  and and_7 (and_7_out, in_3[2], nand_1_out, not_13_out, in_3[0]);
  and and_8 (and_8_out, in_3[1], in_3[2], xor_1_out, not_14_out);
  and and_9 (and_9_out, in_3[2], in_3[1], in_3[0], xnor_1_out);
  or or_2 (out_4, and_2_out, and_3_out, and_4_out, and_5_out, and_6_out, and_7_out, and_8_out, and_9_out);

  // Notes on the sheet:
  //   010 - or
  //   011 - nor
  //   100- and
  //   101 - nand
  //   110 - xor
  //   111 - xnor
  //   000 - not de a 
  //   001 - not de b
endmodule

module exemplo033 (
  input  in_1,
  input  in_2,
  input  in_3,
  output and_nand,
  output or_nor
);

  wire and_1_out, and_2_out, and_3_out, and_4_out, not_1_out, not_2_out, or_and_nor_nand_1_out_3,
       or_and_nor_nand_1_out_4, or_and_nor_nand_1_out_5, or_and_nor_nand_1_out_6;

  or_and_nor_nand or_and_nor_nand_1 (
    .in_1(in_1), .in_2(in_2), .out_3(or_and_nor_nand_1_out_3), .out_4(or_and_nor_nand_1_out_4),
    .out_5(or_and_nor_nand_1_out_5), .out_6(or_and_nor_nand_1_out_6));
  not not_1 (not_1_out, in_3);
  not not_2 (not_2_out, in_3);
  and and_1 (and_1_out, or_and_nor_nand_1_out_3, not_1_out, not_1_out, not_1_out);
  and and_2 (and_2_out, or_and_nor_nand_1_out_4, not_2_out);
  and and_3 (and_3_out, or_and_nor_nand_1_out_5, in_3);
  and and_4 (and_4_out, or_and_nor_nand_1_out_6, in_3, in_3);
  or or_1 (and_nand, and_1_out, and_3_out);
  or or_2 (or_nor, and_2_out, and_4_out);

  // Notes on the sheet:
  //   guilherme alves de oliveira
  //   0 - or/and
  //   1 - nor/nand
endmodule

module or_and_nor_nand (
  input  in_1,
  input  in_2,
  output out_3,
  output out_4,
  output out_5,
  output out_6
);

  and and_1 (out_3, in_1, in_2);
  or or_1 (out_4, in_2, in_1);
  nand nand_1 (out_5, in_2, in_1);
  nor nor_1 (out_6, in_2, in_1);
endmodule
