// Logisim project Exercicio2.circ as structural Verilog: 7 circuits, main circuit main
module main (
  input  a,
  input  b,
  input  chave,
  output s
);

  wire and1_out, and2_out, and3_out, not_1_out, or1_out;

  and and1 (and1_out, a, b);
  or or1 (or1_out, a, b);
  not not_1 (not_1_out, chave);
  and and2 (and2_out, and1_out, chave);
  or or2 (s, and2_out, and3_out);
  and and3 (and3_out, or1_out, not_1_out);

  // Notes on the sheet:
  //   Exercicio 2
  //   Aluno: Isabel Bicalho Amaro
  //   Matricula: 451580
  //   s0
  //   s1
  //   s3
  //   s2
  //   s4
endmodule

module Exercicio_03 (
  input  Chave,
  input  a,
  input  b,
  output s1,
  output s2
);

  wire and1_out, and2_out, and3_out, and4_out, and5_out, nand1_out, nor1_out, not1_2_out, not1_out, or1_out;

  and and1 (and1_out, a, b);
  or or1 (or1_out, a, b);
  not not1 (not1_out, Chave);
  nand nand1 (nand1_out, a, b);
  not not1_2 (not1_2_out, Chave);
  nor nor1 (nor1_out, a, b);
  and and2 (and2_out, not1_out, and1_out);
  and and3 (and3_out, Chave, nand1_out);
  and and4 (and4_out, not1_2_out, or1_out);
  and and5 (and5_out, Chave, nor1_out);
  or or2 (s1, and2_out, and4_out);
  or or3 (s2, and3_out, and5_out);

  // Notes on the sheet:
  //   a1
  //   a2
  //   a3
  //   a4
  //   a5
  //   a6
  //   a7
  //   a8
  //   Exercicio 3
  //   Aluno: Isabel Bicalho Amaro
  //   Matricula: 451580
endmodule

module Exercicio4 (
  input  a,
  input  b,
  input  C1,
  input  C2,
  output s1,
  output s2
);

  wire and1_out, and2_out, and3_out, and4_out, and5_out, and6_out, and7_out, and8_out, nc2_out, nor1_out,
       not_1_out, not_2_out, not_3_out, or1_out, xnor1_out, xor1_out;

  or or1 (or1_out, a, b);
  nor nor1 (nor1_out, a, b);
  xor xor1 (xor1_out, a, b);
  xnor xnor1 (xnor1_out, a, b);
  not not_1 (not_1_out, C1);
  and and1 (and1_out, not_1_out, not_2_out);
  not not_2 (not_2_out, C2);
  not not_3 (not_3_out, C1);
  and and2 (and2_out, not_3_out, C2);
  and and3 (and3_out, C1, nc2_out);
  not nc2 (nc2_out, C2);
  and and4 (and4_out, C1, C2);
  and and5 (and5_out, and1_out, or1_out);
  and and6 (and6_out, and2_out, nor1_out);
  and and7 (and7_out, and3_out, xor1_out);
  and and8 (and8_out, and4_out, xnor1_out);
  or or2 (s1, and5_out, and6_out);
  or or3 (s2, and7_out, and8_out);

  // Notes on the sheet:
  //   a1
  //   a2
  //   a3
  //   a4
  //   nc1
  //   a5
  //   nc2
  //   a6
  //   nc1
  //   a7
  //   a8
  //   Exercicio 4
  //   Aluno: Isabel Bicalho Amaro
  //   Matricula: 451580
  //   a9
  //   a10
  //   a11
  //   a12
endmodule

module Exercicio5 (
  input  [3:0] a,
  input  [3:0] b,
  output [3:0] s1,
  output [3:0] s2,
  output [3:0] s3,
  output [3:0] s4,
  output [3:0] s5,
  output [3:0] s6,
  output [3:0] s7,
  output [3:0] s8
);

  assign s1 = ~a;  // NOT_Gate not_1, 4 bits wide
  assign s2 = ~b;  // NOT_Gate not_2, 4 bits wide
  assign s3 = a | b;  // OR_Gate or_1, 4 bits wide
  assign s4 = ~(a | b);  // NOR_Gate nor_1, 4 bits wide
  assign s5 = a & b;  // AND_Gate and_1, 4 bits wide
  assign s6 = ~(a & b);  // NAND_Gate nand_1, 4 bits wide
  assign s7 = a ^ b;  // XOR_Gate xor_1, 4 bits wide
  assign s8 = ~(a ^ b);  // XNOR_Gate xnor_1, 4 bits wide

  // Notes on the sheet:
  //   Exercicio 5
  //   Aluno: Isabel Bicalho Amaro
  //   Matricula: 451580
endmodule

module Exercicio2__2 (
  input  [3:0] a,
  input  [3:0] b,
  input  Chave,
  input  Chave_2,
  input  Chave_3,
  input  Chave_4,
  output out_7,
  output out_8,
  output out_9,
  output out_10
);

  main main_1 (.a(a[0]), .b(b[0]), .chave(Chave), .s(out_7));
  main main_2 (.a(a[1]), .b(b[1]), .chave(Chave_2), .s(out_8));
  main main_3 (.a(a[2]), .b(b[2]), .chave(Chave_3), .s(out_9));
  main main_4 (.a(a[3]), .b(b[3]), .chave(Chave_4), .s(out_10));

  // Notes on the sheet:
  //   Exercicio 2
  //   Aluno: Isabel Bicalho Amaro
  //   Matricula: 451580
endmodule

module Exercicio3__2 (
  input  Chave,
  input  [3:0] a,
  input  [3:0] b,
  input  Chave_2,
  input  Chave_3,
  input  Chave_4,
  output out_7,
  output out_8,
  output out_9,
  output out_10,
  output out_11,
  output out_12,
  output out_13,
  output out_14
);

  Exercicio_03 exercicio_03_1 (.a(a[0]), .b(b[0]), .Chave(Chave), .s1(out_7), .s2(out_8));
  Exercicio_03 exercicio_03_2 (.a(a[1]), .b(b[1]), .Chave(Chave_2), .s1(out_9), .s2(out_10));
  Exercicio_03 exercicio_03_3 (.a(a[2]), .b(b[2]), .Chave(Chave_3), .s1(out_11), .s2(out_12));
  Exercicio_03 exercicio_03_4 (.a(a[3]), .b(b[3]), .Chave(Chave_4), .s1(out_13), .s2(out_14));

  // Notes on the sheet:
  //   Exercicio 3
  //   Aluno: Isabel Bicalho Amaro
  //   Matricula: 451580
endmodule

module Exercicio4__2 (
  input  [3:0] a,
  input  [3:0] b,
  input  C1,
  input  C1_2,
  input  C1_3,
  input  C1_4,
  input  C1_5,
  input  C1_6,
  input  C1_7,
  input  C1_8,
  output s1,
  output s2,
  output s1_2,
  output s2_2,
  output s1_3,
  output s2_3,
  output s1_4,
  output s2_4
);

  Exercicio4 exercicio4_1 (.a(a[0]), .b(b[0]), .C1(C1), .C2(C1_2), .s1(s1), .s2(s2));
  Exercicio4 exercicio4_2 (.a(a[1]), .b(b[1]), .C1(C1_3), .C2(C1_4), .s1(s1_2), .s2(s2_2));
  Exercicio4 exercicio4_3 (.a(a[2]), .b(b[2]), .C1(C1_5), .C2(C1_6), .s1(s1_3), .s2(s2_3));
  Exercicio4 exercicio4_4 (.a(a[3]), .b(b[3]), .C1(C1_7), .C2(C1_8), .s1(s1_4), .s2(s2_4));

  // Notes on the sheet:
  //   Exercicio 4
  //   Matricula: 451580
  //   Aluno: Isabel Bicalho Amaro
endmodule
