// Logisim project Exemplo0032.circ as structural Verilog: 1 circuit, main circuit main
module main (
  input  X,
  input  Y,
  input  _0___Porta_AND,
  output out_4
);

  wire and_1_out, and_2_out, and_3_out, not_1_out, or_1_out;

  and and_1 (and_1_out, Y, X);
  or or_1 (or_1_out, Y, X);
  not not_1 (not_1_out, _0___Porta_AND);
  and and_2 (and_2_out, and_1_out, not_1_out);
  and and_3 (and_3_out, or_1_out, _0___Porta_AND);
  or or_2 (out_4, and_2_out, and_3_out);

  // Notes on the sheet:
  //   Rodolfo Herman - 451612
  //   1 - Porta OR
endmodule
