// Logisim project Exemplo0034.circ as structural Verilog: 1 circuit, main circuit main
module main (
  input  A,
  input  B,
  input  [1:0] _11___Porta_XNOR,
  output out_4
);

  wire and_1_out, and_2_out, and_3_out, and_4_out, nor_1_out, not_1_out, not_2_out, or_1_out, or_2_out,
       or_3_out, xnor_1_out, xor_1_out;

  or or_1 (or_1_out, B, A);
  nor nor_1 (nor_1_out, B, A);
  xor xor_1 (xor_1_out, B, A);
  xnor xnor_1 (xnor_1_out, B, A);
  not not_1 (not_1_out, _11___Porta_XNOR[1]);
  not not_2 (not_2_out, _11___Porta_XNOR[0]);
  and and_1 (and_1_out, or_1_out, not_1_out, not_2_out);
  and and_2 (and_2_out, nor_1_out, _11___Porta_XNOR[0], not_1_out);
  and and_3 (and_3_out, xor_1_out, not_2_out, _11___Porta_XNOR[1]);
  and and_4 (and_4_out, xnor_1_out, _11___Porta_XNOR[0], _11___Porta_XNOR[1]);
  or or_2 (or_2_out, and_3_out, and_4_out);
  or or_3 (or_3_out, and_1_out, and_2_out);
  or or_4 (out_4, or_3_out, or_2_out);

  // Notes on the sheet:
  //   Rodolfo Herman - 451612
  //   00 - Porta OR
  //   01 - Porta NOR
  //   10 - Porta XOR
endmodule
