// Logisim project Exemplo0034.circ as structural Verilog: 2 circuits, main circuit main
module main (
  input  in_1,
  input  in_2,
  input  [1:0] in_3,
  output out_4
);

  wire and_1_out, and_2_out, and_3_out, and_4_out, and_5_out, and_6_out, not_1_out, not_2_out, not_3_out,
       not_4_out, not_5_out, not_6_out, not_7_out;

  not not_1 (not_1_out, in_1);
  not not_2 (not_2_out, in_2);
  not not_3 (not_3_out, in_3[1]);
  and and_1 (and_1_out, not_1_out, not_2_out, in_3[0]);
  and and_2 (and_2_out, in_1, not_3_out, not_4_out);
  not not_4 (not_4_out, in_3[0]);
  not not_5 (not_5_out, in_1);
  not not_6 (not_6_out, in_3[0]);
  and and_3 (and_3_out, in_3[0], in_3[1], in_2, in_1);
  not not_7 (not_7_out, in_2);
  and and_4 (and_4_out, in_2, not_3_out, not_4_out);
  and and_5 (and_5_out, not_5_out, in_2, in_3[1], not_6_out);
  and and_6 (and_6_out, not_7_out, in_1, in_3[1], not_6_out);
  or or_1 (out_4, and_4_out, and_1_out, and_5_out, and_3_out, and_2_out, and_6_out);

  // Notes on the sheet:
  //   Exemplo0034
  //   Nome: Tiago Matta Machado Zaidan
  //   Matricula: 451620
  //   00-or       01-nor       10-xor        11-xnor
endmodule

module LU (
  input  in_1,
  input  in_2,
  output out_3,
  output out_4,
  output out_5,
  output out_6
);

  or or_1 (out_3, in_1, in_2);
  nor nor_1 (out_4, in_1, in_2);
  xor xor_1 (out_5, in_1, in_2);
  xnor xnor_1 (out_6, in_1, in_2);
endmodule
