// Logisim project Exemplo0032.circ as structural Verilog: 1 circuit, main circuit main
module main (
  input  x,
  input  y,
  input  z,
  output S
);

  wire and_1_out, and_2_out, and_3_out, not_1_out, or_1_out;

  and and_1 (and_1_out, x, y);
  or or_1 (or_1_out, x, y);
  not not_1 (not_1_out, z);
  and and_2 (and_2_out, and_1_out, z);
  and and_3 (and_3_out, or_1_out, not_1_out);
  or or_2 (S, and_2_out, and_3_out);
endmodule
