// Logisim project Exemplo0033.circ as structural Verilog: 1 circuit, main circuit main
module main (
  input  in_1,
  input  in_2,
  input  in_3,
  output out_4,
  output out_5,
  output out_6,
  output out_7
);

  wire and_1_out, nand_1_out, nor_1_out, not_1_out, not_2_out, or_1_out;

  and and_1 (and_1_out, in_2, in_1);
  or or_1 (or_1_out, in_1, in_2);
  nand nand_1 (nand_1_out, in_1, in_2);
  nor nor_1 (nor_1_out, in_1, in_2);
  not not_1 (not_1_out, in_3);
  not not_2 (not_2_out, in_3);
  and and_2 (out_4, and_1_out, not_1_out);
  and and_3 (out_5, or_1_out, not_2_out);
  and and_4 (out_6, in_3, nand_1_out);
  and and_5 (out_7, in_3, nor_1_out);
endmodule
