// Logisim project Exemplo0035.circ as structural Verilog: 1 circuit, main circuit main
module main (
  input  in_1,
  input  in_2,
  input  in_3,
  input  in_4,
  input  in_5,
  output out_6,
  output out_7,
  output out_8,
  output out_9,
  output out_10,
  output out_11,
  output out_12,
  output out_13
);

  wire and_1_out, nand_1_out, nor_1_out, not_1_out, not_2_out, not_3_out, not_4_out, not_5_out, not_6_out,
       not_7_out, not_8_out, not_9_out, not_10_out, not_11_out, not_12_out, not_13_out, not_14_out, or_1_out,
       xnor_1_out, xor_1_out;

  not not_1 (not_1_out, in_2);
  not not_2 (not_2_out, in_1);
  or or_1 (or_1_out, in_2, in_1);
  and and_1 (and_1_out, in_2, in_1);
  nor nor_1 (nor_1_out, in_2, in_1);
  nand nand_1 (nand_1_out, in_2, in_1);
  xor xor_1 (xor_1_out, in_2, in_1);
  xnor xnor_1 (xnor_1_out, in_1, in_2);
  not not_3 (not_3_out, in_3);
  not not_4 (not_4_out, in_4);
  not not_5 (not_5_out, in_5);
  not not_6 (not_6_out, in_3);
  not not_7 (not_7_out, in_4);
  not not_8 (not_8_out, in_3);
  not not_9 (not_9_out, in_5);
  not not_10 (not_10_out, in_3);
  not not_11 (not_11_out, in_4);
  not not_12 (not_12_out, in_5);
  not not_13 (not_13_out, in_4);
  not not_14 (not_14_out, in_5);
  and and_2 (out_6, not_3_out, not_4_out, not_5_out, not_1_out);
  and and_3 (out_7, not_2_out, not_6_out, not_7_out, in_5);
  and and_4 (out_8, or_1_out, not_8_out, in_4, not_9_out);
  and and_5 (out_9, nor_1_out, not_10_out, in_4, in_5);
  and and_6 (out_10, and_1_out, in_3, not_11_out, not_12_out);
  and and_7 (out_11, in_3, nand_1_out, not_13_out, in_5);
  and and_8 (out_12, in_3, xor_1_out, in_4, not_14_out);
  and and_9 (out_13, in_3, in_4, xnor_1_out, in_5);
endmodule
