// Logisim project Exemplo0033.circ as structural Verilog: 1 circuit, main circuit main
module main (
  input  a,
  input  b,
  input  c,
  output out_4,
  output out_5
);

  wire and_1_out, and_2_out, and_3_out, and_4_out, and_5_out, nand_1_out, nor_1_out, not_1_out, not_2_out,
       or_1_out;

  and and_1 (and_1_out, a, a, b);
  or or_1 (or_1_out, a, b);
  nand nand_1 (nand_1_out, a, b);
  nor nor_1 (nor_1_out, a, b);
  and and_2 (and_2_out, c, and_1_out);
  and and_3 (and_3_out, c, or_1_out);
  not not_1 (not_1_out, c);
  and and_4 (and_4_out, not_1_out, nand_1_out);
  not not_2 (not_2_out, c);
  and and_5 (and_5_out, not_2_out, nor_1_out);
  or or_2 (out_4, and_2_out, and_4_out);
  or or_3 (out_5, and_3_out, and_5_out);

  // Notes on the sheet:
  //   c
  //   0                and ou or
  //   1                nand ou nor
endmodule
