// Logisim project Exemplo0034.circ as structural Verilog: 1 circuit, main circuit main
module main (
  input  a,
  input  b,
  input  [1:0] chave,
  output s
);

  wire and_1_out, and_2_out, and_3_out, and_4_out, nor_1_out, not_1_out, not_2_out, not_3_out, not_4_out,
       or_1_out, xnor_1_out, xor_1_out;

  or or_1 (or_1_out, a, b);
  nor nor_1 (nor_1_out, a, b);
  xor xor_1 (xor_1_out, a, b);
  xnor xnor_1 (xnor_1_out, a, b);
  not not_1 (not_1_out, chave[1]);
  and and_1 (and_1_out, or_1_out, not_1_out, not_2_out);
  not not_2 (not_2_out, chave[0]);
  and and_2 (and_2_out, nor_1_out, not_3_out, chave[0]);
  not not_3 (not_3_out, chave[1]);
  and and_3 (and_3_out, xor_1_out, chave[1], not_4_out);
  not not_4 (not_4_out, chave[0]);
  and and_4 (and_4_out, xnor_1_out, chave[1], chave[0]);
  or or_2 (s, and_1_out, and_2_out, and_3_out, and_4_out);

  // Notes on the sheet:
  //   chave
  //   operação
  //   00                or
  //   01               nor
  //   10                xor
  //   11                xnor
endmodule
