// Logisim project Exemplo0036.circ as structural Verilog: 1 circuit, main circuit main
module main (
  input  a,
  input  b,
  input  chave,
  output s
);

  wire xor_1_out, xor_2_out;

  xor xor_1 (xor_1_out, b, a);
  xor xor_2 (xor_2_out, xor_1_out, chave);
  not not_1 (s, xor_2_out);

  // Notes on the sheet:
  //   chave
  //   saida
  //   0                  1-se igual    0-se diferente
  //   1                  0-se igual    1-se diferente
endmodule
