// Logisim project Exemplo0031.circ as structural Verilog: 1 circuit, main circuit Exemplo0031
module Exemplo0031 (
  input  a0,
  input  a1,
  input  a2,
  input  a3,
  input  b0,
  input  b1,
  input  b2,
  input  b3,
  output out_9,
  output out_10,
  output out_11,
  output out_12,
  output out_13,
  output out_14,
  output out_15,
  output out_16
);

  and and_1 (out_9, b0, a0);
  and and_2 (out_10, b1, a1);
  and and_3 (out_11, b2, a2);
  and and_4 (out_12, b3, a3);
  or or_1 (out_13, b0, a0);
  or or_2 (out_14, b1, a1);
  or or_3 (out_15, b2, a2);
  or or_4 (out_16, b3, a3);
endmodule
