// Logisim project Exemplo0032.circ as structural Verilog: 1 circuit, main circuit main
module main (
  input  a,
  input  b,
  input  chave,
  output s_AND,
  output s_OR
);

  wire and_1_out, not_1_out, or_1_out;

  and and_1 (and_1_out, b, a);
  or or_1 (or_1_out, b, a);
  not not_1 (not_1_out, chave);
  and and_2 (s_AND, and_1_out, chave);
  and and_3 (s_OR, or_1_out, not_1_out);
endmodule
