// Logisim project Exemplo0036.circ as structural Verilog: 1 circuit, main circuit main
module main (
  input  a,
  input  b,
  input  chave,
  output s0,
  output s1
);

  wire not_1_out, xnor_1_out, xor_1_out;

  xor xor_1 (xor_1_out, a, b);
  xnor xnor_1 (xnor_1_out, a, b);
  not not_1 (not_1_out, chave);
  and and_1 (s0, xor_1_out, chave);
  and and_2 (s1, xnor_1_out, not_1_out);

  // Notes on the sheet:
  //   s0 -> Diferente (chave = 1)
  //   s1 -> Igual (chave = 0)
endmodule
