// Logisim project exe-0021, 0022, 0025 e extra-06.circ as structural Verilog: 7 circuits, main circuit HALF-ADDER
// H.A
module HALF_ADDER (
  input  A,
  input  B,
  output S0,
  output S1
);

  xor xor_1 (S0, B, A);
  and and_1 (S1, B, A);
endmodule

// F/A
module FULL_ADDER (
  input  A,
  input  B,
  input  CARRY_IN,
  output S0,
  output S1
);

  wire half_adder_1_s0, half_adder_1_s1, half_adder_2_s1;

  HALF_ADDER half_adder_1 (.A(A), .B(B), .S0(half_adder_1_s0), .S1(half_adder_1_s1));
  HALF_ADDER half_adder_2 (.A(half_adder_1_s0), .B(CARRY_IN), .S0(S0), .S1(half_adder_2_s1));
  or or_1 (S1, half_adder_1_s1, half_adder_2_s1);
endmodule

// F/A
module FULL_ADDER_3bits (
  input  [2:0] A,
  input  [2:0] B,
  input  CARRY_IN,
  output OVERFLOW,
  output [2:0] SOMA
);

  wire full_adder_1_s1, full_adder_2_s1;

  // Probe on A
  // Probe on B
  FULL_ADDER full_adder_1 (.A(A[0]), .B(B[0]), .CARRY_IN(CARRY_IN), .S0(SOMA[0]), .S1(full_adder_1_s1));
  FULL_ADDER full_adder_2 (.A(A[1]), .B(B[1]), .CARRY_IN(full_adder_1_s1), .S0(SOMA[1]), .S1(full_adder_2_s1));
  FULL_ADDER full_adder_3 (.A(A[2]), .B(B[2]), .CARRY_IN(full_adder_2_s1), .S0(SOMA[2]), .S1(OVERFLOW));
  // Probe on SOMA
endmodule

module exercicio0021 (
  input  [2:0] A,
  input  [2:0] B,
  input  CARRY_IN,
  output OVERFLOW,
  output [2:0] out_5
);

  // Probe on A
  // Probe on B
  FULL_ADDER_3bits full_adder_3bits_1 (.A(A), .B(B), .CARRY_IN(CARRY_IN), .OVERFLOW(OVERFLOW), .SOMA(out_5));
  // Probe on out_5

  // Notes on the sheet:
  //   Exercicio-0021
  //   Milton costa teles da silva - 002751
endmodule

module exercicio_0022 (
  input  [1:0] A,
  input  [1:0] B,
  input  CARRY_IN,
  output [2:0] out_4
);

  wire full_adder_1_s1, full_adder_2_s1, xor_1_out, xor_2_out;

  // Probe on A
  // Probe on B
  xor xor_1 (xor_1_out, CARRY_IN, B[0]);
  FULL_ADDER full_adder_1 (.A(A[0]), .B(xor_1_out), .CARRY_IN(CARRY_IN), .S0(out_4[0]), .S1(full_adder_1_s1));
  xor xor_2 (xor_2_out, CARRY_IN, B[1]);
  FULL_ADDER full_adder_2 (.A(A[1]), .B(xor_2_out), .CARRY_IN(full_adder_1_s1), .S0(out_4[1]), .S1(full_adder_2_s1));
  xor xor_3 (out_4[2], full_adder_2_s1, CARRY_IN);
  // Probe on out_4

  // Notes on the sheet:
  //   1-SUBTRACTOR
  //   Exercicio-0022
  //   Milton costa teles da silva - 002751
endmodule

module extra_01 (
  input  [1:0] A,
  input  [1:0] B,
  input  CARRY_IN,
  output [2:0] out_4
);

  wire full_adder_1_s1, full_adder_2_s1, xor_1_out, xor_2_out;

  // Probe on A
  // Probe on B
  xor xor_1 (xor_1_out, CARRY_IN, B[0]);
  FULL_ADDER full_adder_1 (.A(A[0]), .B(xor_1_out), .CARRY_IN(CARRY_IN), .S0(out_4[0]), .S1(full_adder_1_s1));
  xor xor_2 (xor_2_out, CARRY_IN, B[1]);
  FULL_ADDER full_adder_2 (.A(A[1]), .B(xor_2_out), .CARRY_IN(full_adder_1_s1), .S0(out_4[1]), .S1(full_adder_2_s1));
  xor xor_3 (out_4[2], full_adder_2_s1, CARRY_IN);
  // Probe on out_4

  // Notes on the sheet:
  //   0-ADDER
  //   1-SUBTRACTOR
  //   Extra-01
  //   Milton costa teles da silva - 002751
endmodule

module exercicio_0025 (
  input  [2:0] A,
  output OVERFLOW,
  output [2:0] s1
);

  wire full_adder_1_s1, full_adder_2_s1;
  wire [2:0] not_1_out;

  // Probe on A
  assign not_1_out = ~A;  // NOT_Gate not_1, 3 bits wide
  FULL_ADDER full_adder_1 (.A(not_1_out[0]), .B(1'b0), .CARRY_IN(1'b1), .S0(s1[0]), .S1(full_adder_1_s1));
  FULL_ADDER full_adder_2 (.A(not_1_out[1]), .B(1'b0), .CARRY_IN(full_adder_1_s1), .S0(s1[1]), .S1(full_adder_2_s1));
  FULL_ADDER full_adder_3 (.A(not_1_out[2]), .B(1'b0), .CARRY_IN(full_adder_2_s1), .S0(s1[2]), .S1(OVERFLOW));
  // Probe on s1

  // Notes on the sheet:
  //   Exercicio-0025
  //   Milton costa teles da silva - 002751
endmodule
