// Logisim project exe-0023 , exe-0024 e extra-07.circ as structural Verilog: 3 circuits, main circuit exercicio0023
module exercicio0023 (
  input  [2:0] A,
  input  [2:0] B,
  output out_3
);

  wire [2:0] xnor_1_out;

  assign xnor_1_out = ~(A ^ B);  // XNOR_Gate xnor_1, 3 bits wide
  and and_1 (out_3, xnor_1_out[0], xnor_1_out[1], xnor_1_out[2]);

  // Notes on the sheet:
  //   EXERCICIO0023
  //   Milton costa teles da silva-02751
endmodule

module exercicio0024 (
  input  [2:0] A,
  input  [2:0] B,
  output S0
);

  wire [2:0] xnor_1_out;

  assign xnor_1_out = ~(A ^ B);  // XNOR_Gate xnor_1, 3 bits wide
  nand nand_1 (S0, xnor_1_out[0], xnor_1_out[1], xnor_1_out[2]);

  // Notes on the sheet:
  //   EXERCICIO0024
  //   Milton costa teles da silva-02751
endmodule

module extra_02 (
  input  CHAVE,
  input  [2:0] A,
  input  [2:0] B,
  output S0
);

  wire and_1_out;
  wire [2:0] xnor_1_out;

  assign xnor_1_out = ~(A ^ B);  // XNOR_Gate xnor_1, 3 bits wide
  and and_1 (and_1_out, xnor_1_out[0], xnor_1_out[1], xnor_1_out[2]);
  xor xor_1 (S0, and_1_out, CHAVE);

  // Notes on the sheet:
  //   Extra_02
  //   Milton costa teles da silva-02751
  //   0_IGUAL
  //   1_DIFERENTE
endmodule
