// Logisim project Exemplo0021.circ as structural Verilog: 1 circuit, main circuit main
module main (
  input  x,
  input  y,
  input  carry_in,
  output s0,
  output s1
);

  wire and_1_out, and_2_out, and_3_out, xor_1_out;

  xor xor_1 (xor_1_out, x, y);
  and and_1 (and_1_out, y, carry_in);
  and and_2 (and_2_out, x, carry_in);
  and and_3 (and_3_out, x, y);
  xor xor_2 (s0, xor_1_out, carry_in);
  or or_1 (s1, and_1_out, and_2_out, and_3_out);
endmodule
