// Logisim project Exemplo0022.circ as structural Verilog: 1 circuit, main circuit main
module main (
  input  a,
  input  b,
  input  carry_in,
  output s0,
  output s1
);

  wire and_1_out, and_2_out, not_1_out, xor_1_out, xor_2_out;

  xor xor_1 (xor_1_out, b, carry_in);
  and and_1 (and_1_out, b, carry_in);
  xor xor_2 (xor_2_out, a, b);
  not not_1 (not_1_out, a);
  and and_2 (and_2_out, xor_1_out, not_1_out);
  xor xor_3 (s1, xor_2_out, carry_in);
  or or_1 (s0, and_2_out, and_1_out);
endmodule
