// Logisim project Exemplo0027.circ as structural Verilog: 3 circuits, main circuit main
module main (
  input  a,
  input  b,
  input  c,
  input  chave,
  output s_IG,
  output s_DIF
);

  wire \diferença_1_out_4 , igualdade_1_out_4, not_1_out;

  Igualdade igualdade_1 (.a(a), .b(b), .c(c), .out_4(igualdade_1_out_4));
  \Diferença  \diferença_1  (.a(a), .b(b), .c(c), .out_4(\diferença_1_out_4 ));
  and and_1 (s_IG, igualdade_1_out_4, not_1_out);
  not not_1 (not_1_out, chave);
  and and_2 (s_DIF, \diferença_1_out_4 , chave);

  // Notes on the sheet:
  //   Igualdade -> chave = 0
  //   Diferença -> chave = 1
endmodule

// IGUAL
module Igualdade (
  input  a,
  input  b,
  input  c,
  output out_4
);

  wire and_1_out, and_2_out, not_1_out, not_2_out, not_3_out;

  not not_1 (not_1_out, a);
  not not_2 (not_2_out, b);
  not not_3 (not_3_out, c);
  and and_1 (and_1_out, not_1_out, not_2_out, not_3_out);
  and and_2 (and_2_out, a, b, c);
  or or_1 (out_4, and_1_out, and_2_out);
endmodule

// DIF
module \Diferença  (
  input  a,
  input  b,
  input  c,
  output out_4
);

  wire and_1_out, and_2_out, not_1_out, not_2_out, xor_1_out;

  not not_1 (not_1_out, a);
  not not_2 (not_2_out, c);
  xor xor_1 (xor_1_out, a, b);
  and and_1 (and_1_out, not_1_out, c);
  and and_2 (and_2_out, b, not_2_out);
  or or_1 (out_4, xor_1_out, and_1_out, and_2_out);
endmodule
