// Logisim project Exemplo0021.circ as structural Verilog: 2 circuits, main circuit main
module main (
  input  [2:0] a,
  input  [2:0] b,
  input  carry_in,
  output Over_flow,
  output [2:0] out_5
);

  wire fulladder_2_s1, fulladder_3_s1;

  FullAdder fulladder_1 (.s1(Over_flow), .x(a[2]), .y(b[2]), .s0(out_5[2]), .carry_in(fulladder_2_s1));
  FullAdder fulladder_2 (.s1(fulladder_2_s1), .x(a[1]), .y(b[1]), .s0(out_5[1]), .carry_in(fulladder_3_s1));
  FullAdder fulladder_3 (.s1(fulladder_3_s1), .x(a[0]), .y(b[0]), .s0(out_5[0]), .carry_in(carry_in));
endmodule

// F.A
module FullAdder (
  input  carry_in,
  input  x,
  input  y,
  output s0,
  output s1
);

  wire and_1_out, and_2_out, and_3_out, xor_1_out;

  xor xor_1 (xor_1_out, x, y);
  and and_1 (and_1_out, y, carry_in);
  and and_2 (and_2_out, x, carry_in);
  and and_3 (and_3_out, x, y);
  xor xor_2 (s0, xor_1_out, carry_in);
  or or_1 (s1, and_1_out, and_2_out, and_3_out);
endmodule
