// Logisim project Exemplo0022.circ as structural Verilog: 5 circuits, main circuit Complemento de 2
// C2
module Complemento_de_2 (
  input  [2:0] a,
  output s2,
  output s1,
  output s0,
  output carry_out
);

  wire half_adder1_1_s1, half_adder2_1_s1;
  wire [2:0] not_1_out;

  assign not_1_out = ~a;  // NOT_Gate not_1, 3 bits wide
  Half_Adder1 half_adder1_1 (.a(not_1_out[0]), .s0(s0), .s1(half_adder1_1_s1));
  Half_Adder2 half_adder2_1 (.a(not_1_out[1]), .b(half_adder1_1_s1), .s0(s1), .s1(half_adder2_1_s1));
  Half_Adder2 half_adder2_2 (.a(not_1_out[2]), .b(half_adder2_1_s1), .s0(s2), .s1(carry_out));
endmodule

// HA1
module Half_Adder1 (
  input  a,
  output s0,
  output s1
);

  xor xor_1 (s0, a, 1'b1);
  and and_1 (s1, a, 1'b1);
endmodule

// HA2
module Half_Adder2 (
  input  a,
  input  b,
  output s0,
  output s1
);

  xor xor_1 (s0, a, b);
  and and_1 (s1, a, b);
endmodule

// F.A.
module Full_Adder (
  input  a,
  input  b,
  input  carryIn,
  output carryOut,
  output s
);

  wire half_adder2_1_s0, half_adder2_1_s1, half_adder2_2_s1;

  or or_1 (carryOut, half_adder2_1_s1, half_adder2_2_s1);
  Half_Adder2 half_adder2_1 (.a(a), .b(b), .s0(half_adder2_1_s0), .s1(half_adder2_1_s1));
  Half_Adder2 half_adder2_2 (.a(half_adder2_1_s0), .b(carryIn), .s0(s), .s1(half_adder2_2_s1));
endmodule

module Full_Sub (
  input  [2:0] a,
  input  [2:0] b,
  output out_3,
  output out_4,
  output out_5,
  output out_6
);

  wire complemento_de_2_1_carry_out, complemento_de_2_1_s0, complemento_de_2_1_s1, complemento_de_2_1_s2,
       full_adder_2_carryout, full_adder_3_carryout;

  Full_Adder full_adder_1 (
    .carryOut(out_3), .a(a[2]), .b(complemento_de_2_1_s2), .s(out_4), .carryIn(full_adder_2_carryout));
  Complemento_de_2 complemento_de_2_1 (
    .a(b), .s2(complemento_de_2_1_s2), .s1(complemento_de_2_1_s1), .s0(complemento_de_2_1_s0),
    .carry_out(complemento_de_2_1_carry_out));
  Full_Adder full_adder_2 (
    .carryOut(full_adder_2_carryout), .a(a[1]), .b(complemento_de_2_1_s1), .s(out_5),
    .carryIn(full_adder_3_carryout));
  Full_Adder full_adder_3 (
    .carryOut(full_adder_3_carryout), .a(a[0]), .b(complemento_de_2_1_s0), .s(out_6),
    .carryIn(complemento_de_2_1_carry_out));
endmodule
