// Logisim project Exemplo0023.circ as structural Verilog: 1 circuit, main circuit main
module main (
  input  [2:0] a,
  input  [2:0] b,
  output s
);

  wire [2:0] xnor_1_out;

  assign xnor_1_out = ~(a ^ b);  // XNOR_Gate xnor_1, 3 bits wide
  and and_1 (s, xnor_1_out[0], xnor_1_out[1], xnor_1_out[2]);
endmodule
