// Logisim project Exemplo0024.circ as structural Verilog: 1 circuit, main circuit main
module main (
  input  [2:0] a,
  input  [2:0] b,
  output s
);

  wire [2:0] xor_1_out;

  assign xor_1_out = a ^ b;  // XOR_Gate xor_1, 3 bits wide
  or or_1 (s, xor_1_out[0], xor_1_out[1], xor_1_out[2]);
endmodule
