// Logisim project Exemplo0025.circ as structural Verilog: 3 circuits, main circuit Complemento de 2
module Complemento_de_2 (
  input  [2:0] a,
  output s2,
  output s1,
  output s0,
  output carry_out
);

  wire half_adder1_1_s1, half_adder2_1_s1;
  wire [2:0] not_1_out;

  assign not_1_out = ~a;  // NOT_Gate not_1, 3 bits wide
  Half_Adder1 half_adder1_1 (.a(not_1_out[0]), .s0(s0), .s1(half_adder1_1_s1));
  Half_Adder2 half_adder2_1 (.a(not_1_out[1]), .b(half_adder1_1_s1), .s0(s1), .s1(half_adder2_1_s1));
  Half_Adder2 half_adder2_2 (.a(not_1_out[2]), .b(half_adder2_1_s1), .s0(s2), .s1(carry_out));
endmodule

// HA1
module Half_Adder1 (
  input  a,
  output s0,
  output s1
);

  xor xor_1 (s0, a, 1'b1);
  and and_1 (s1, a, 1'b1);
endmodule

// HA2
module Half_Adder2 (
  input  a,
  input  b,
  output s0,
  output s1
);

  xor xor_1 (s0, a, b);
  and and_1 (s1, a, b);
endmodule
