// Logisim project Exemplo0027.circ as structural Verilog: 3 circuits, main circuit main
module main (
  input  [2:0] a,
  input  [2:0] b,
  input  chave,
  output s_IG,
  output s_DIF
);

  wire \diferença_1_s , igualdade_1_s, not_1_out;

  Igualdade igualdade_1 (.a(a), .b(b), .s(igualdade_1_s));
  \Diferença  \diferença_1  (.a(a), .b(b), .s(\diferença_1_s ));
  and and_1 (s_IG, igualdade_1_s, not_1_out);
  not not_1 (not_1_out, chave);
  and and_2 (s_DIF, \diferença_1_s , chave);

  // Notes on the sheet:
  //   Igualdade -> chave = 0
  //   Diferença -> chave = 1
endmodule

// IGUAL
module Igualdade (
  input  [2:0] a,
  input  [2:0] b,
  output s
);

  wire [2:0] xnor_1_out;

  assign xnor_1_out = ~(a ^ b);  // XNOR_Gate xnor_1, 3 bits wide
  and and_1 (s, xnor_1_out[0], xnor_1_out[1], xnor_1_out[2]);
endmodule

// DIF
module \Diferença  (
  input  [2:0] a,
  input  [2:0] b,
  output s
);

  wire [2:0] xor_1_out;

  assign xor_1_out = a ^ b;  // XOR_Gate xor_1, 3 bits wide
  or or_1 (s, xor_1_out[0], xor_1_out[1], xor_1_out[2]);
endmodule
