// Logisim project Exemplo0023.circ as structural Verilog: 1 circuit, main circuit main
module main (
  input  X2,
  input  X1,
  input  X0,
  input  Y0,
  input  Y2,
  input  Y1,
  output out_7
);

  wire or_1_out, or_2_out, xor_1_out, xor_2_out, xor_3_out;

  xor xor_1 (xor_1_out, X0, Y0);
  xor xor_2 (xor_2_out, X1, Y1);
  xor xor_3 (xor_3_out, X2, Y2);
  or or_1 (or_1_out, xor_1_out, xor_2_out);
  or or_2 (or_2_out, or_1_out, xor_3_out);
  not not_1 (out_7, or_2_out);

  // Notes on the sheet:
  //   Rodolfo Herman 451612
  //   Comparador de Igualdade
  //   Iguais = 1
  //   Diferentes = 0
endmodule
