// Logisim project Exemplo0021.circ as structural Verilog: 2 circuits, main circuit half adder
// HA
module half_adder (
  input  [2:0] A,
  input  [2:0] B,
  output [2:0] S,
  output [2:0] C_OUT
);

  assign S = A ^ B;  // XOR_Gate xor_1, 3 bits wide
  assign C_OUT = A & B;  // AND_Gate and_1, 3 bits wide

  // Notes on the sheet:
  //   Guia 04 - Half Adder
  //   João Henrique - 392734
endmodule

module full_adder (
  input  [2:0] C_IN,
  input  [2:0] A,
  input  [2:0] B,
  output [2:0] out_4,
  output [2:0] out_5
);

  wire [2:0] half_adder_1_c_out, half_adder_1_s, half_adder_2_c_out;

  half_adder half_adder_1 (.A(A), .B(B), .C_OUT(half_adder_1_c_out), .S(half_adder_1_s));
  half_adder half_adder_2 (.A(C_IN), .B(half_adder_1_s), .C_OUT(half_adder_2_c_out), .S(out_4));
  assign out_5 = half_adder_2_c_out | half_adder_1_c_out;  // OR_Gate or_1, 3 bits wide

  // Notes on the sheet:
  //   Guia 04 - Full Adder
  //   João Henrique - 392734
endmodule
