// Logisim project Exemplo0022.circ as structural Verilog: 2 circuits, main circuit half subtrator
module half_subtrator (
  input  [2:0] A,
  input  [2:0] B,
  output [2:0] S,
  output [2:0] C_OUT
);

  wire [2:0] not_1_out;

  assign not_1_out = ~A;  // NOT_Gate not_1, 3 bits wide
  assign S = B ^ A;  // XOR_Gate xor_1, 3 bits wide
  assign C_OUT = B & not_1_out;  // AND_Gate and_1, 3 bits wide
endmodule

module full_adder (
  input  [2:0] A,
  input  [2:0] B,
  input  [2:0] C_IN,
  output [2:0] S,
  output [2:0] C_OUT
);

  wire [2:0] half_subtrator_1_c_out, half_subtrator_1_s, half_subtrator_2_c_out;

  half_subtrator half_subtrator_1 (.A(A), .B(B), .C_OUT(half_subtrator_1_c_out), .S(half_subtrator_1_s));
  half_subtrator half_subtrator_2 (.A(half_subtrator_1_s), .B(C_IN), .C_OUT(half_subtrator_2_c_out), .S(S));
  assign C_OUT = half_subtrator_2_c_out | half_subtrator_1_c_out;  // OR_Gate or_1, 3 bits wide
endmodule
