// Logisim project Exemplo0025.circ as structural Verilog: 2 circuits, main circuit half adder
// HA
module half_adder (
  input  [2:0] A,
  input  [2:0] B,
  output [2:0] S,
  output [2:0] C_OUT
);

  assign S = A ^ B;  // XOR_Gate xor_1, 3 bits wide
  assign C_OUT = A & B;  // AND_Gate and_1, 3 bits wide

  // Notes on the sheet:
  //   João Henrique - 392734
endmodule

module complemento_de_2 (
  input  [2:0] plus_1,
  input  [2:0] Sinal_P,
  input  [2:0] P4,
  input  [2:0] P3,
  input  [2:0] P2,
  input  [2:0] P1,
  input  [2:0] P0,
  output [2:0] S0,
  output [2:0] S1,
  output [2:0] S2,
  output [2:0] S3,
  output [2:0] S4,
  output [2:0] Sinal
);

  wire [2:0] half_adder_1_c_out, half_adder_3_c_out, half_adder_4_c_out, half_adder_5_c_out,
       half_adder_6_c_out, not_1_out, not_2_out, not_3_out, not_4_out, not_5_out, not_6_out;

  assign not_1_out = ~P4;  // NOT_Gate not_1, 3 bits wide
  assign not_2_out = ~Sinal_P;  // NOT_Gate not_2, 3 bits wide
  half_adder half_adder_1 (.A(half_adder_4_c_out), .B(not_1_out), .C_OUT(half_adder_1_c_out), .S(S4));
  half_adder half_adder_2 (.A(half_adder_1_c_out), .B(not_2_out), .S(Sinal));  // open: C_OUT
  assign not_3_out = ~P2;  // NOT_Gate not_3, 3 bits wide
  assign not_4_out = ~P3;  // NOT_Gate not_4, 3 bits wide
  half_adder half_adder_3 (.A(half_adder_6_c_out), .B(not_3_out), .C_OUT(half_adder_3_c_out), .S(S2));
  half_adder half_adder_4 (.A(half_adder_3_c_out), .B(not_4_out), .C_OUT(half_adder_4_c_out), .S(S3));
  assign not_5_out = ~P1;  // NOT_Gate not_5, 3 bits wide
  assign not_6_out = ~P0;  // NOT_Gate not_6, 3 bits wide
  half_adder half_adder_5 (.A(plus_1), .B(not_6_out), .C_OUT(half_adder_5_c_out), .S(S0));
  half_adder half_adder_6 (.A(half_adder_5_c_out), .B(not_5_out), .C_OUT(half_adder_6_c_out), .S(S1));

  // Notes on the sheet:
  //   Exemplo0025 - João Henrique Mendes de Oliveira - 392734
endmodule
