// Logisim project Exemplo0026.circ as structural Verilog: 1 circuit, main circuit main
module main (
  input  [5:0] A,
  input  [5:0] B,
  input  [5:0] CarryIn,
  output [5:0] S1,
  output [5:0] S2,
  output [5:0] S3,
  output [5:0] S4
);

  wire [5:0] _1_2_out, _1_out, _2_2_out, _2_out, _3_out, _4_out, _5_out, _6_out, _7_out, _8_out, _9_out,
       _10_out, NOT1_out, NOT2_out, NOT3_out;

  assign NOT1_out = ~CarryIn;  // NOT_Gate NOT1, 6 bits wide
  assign _1_out = CarryIn & B;  // AND_Gate _1, 6 bits wide
  assign _2_out = CarryIn & A;  // AND_Gate _2, 6 bits wide
  assign _3_out = NOT1_out & B;  // AND_Gate _3, 6 bits wide
  assign _4_out = NOT1_out & NOT2_out;  // AND_Gate _4, 6 bits wide
  assign NOT2_out = ~A;  // NOT_Gate NOT2, 6 bits wide
  assign _5_out = {6{1'b1}} & CarryIn;  // AND_Gate _5, 6 bits wide
  assign _7_out = {6{1'b1}} & NOT1_out;  // AND_Gate _7, 6 bits wide
  assign _1_2_out = _2_out ^ _1_out;  // XOR_Gate _1_2, 6 bits wide
  assign _6_out = _1_out & _2_out;  // AND_Gate _6, 6 bits wide
  assign _2_2_out = _4_out ^ _3_out;  // XOR_Gate _2_2, 6 bits wide
  assign _8_out = _3_out & _4_out;  // AND_Gate _8, 6 bits wide
  assign S1 = _5_out ^ _1_2_out;  // XOR_Gate _3_2, 6 bits wide
  assign _9_out = _5_out & _1_2_out;  // AND_Gate _9, 6 bits wide
  assign S3 = _7_out ^ _2_2_out;  // XOR_Gate _4_2, 6 bits wide
  assign _10_out = _7_out & NOT3_out;  // AND_Gate _10, 6 bits wide
  assign NOT3_out = ~_2_2_out;  // NOT_Gate NOT3, 6 bits wide
  assign S2 = _9_out | _6_out;  // OR_Gate _1_3, 6 bits wide
  assign S4 = _10_out | _8_out;  // OR_Gate _2_3, 6 bits wide

  // Notes on the sheet:
  //   Exemplo0026 - João Henrique Mendes de Oliveira - 392734
endmodule
