// Logisim project Exemplo0021.v.circ as structural Verilog: 5 circuits, main circuit main
module main (
  input  in_1,
  input  in_2,
  output out_3,
  output out_4
);

  xor xor_1 (out_3, in_2, in_1);
  and and_1 (out_4, in_1, in_2);
endmodule

module MeiaSoma (
  input  in_1,
  input  in_2,
  output out_3,
  output out_4
);

  xor xor_1 (out_3, in_2, in_1);
  and and_1 (out_4, in_1, in_2);
endmodule

module VaiUM (
  input  in_1,
  input  in_2,
  input  in_3,
  output out_4,
  output out_5
);

  wire and_1_out, meiasoma_1_out_3, meiasoma_1_out_4;

  MeiaSoma meiasoma_1 (.in_1(in_2), .in_2(in_1), .out_3(meiasoma_1_out_3), .out_4(meiasoma_1_out_4));
  and and_1 (and_1_out, in_3, meiasoma_1_out_3);
  xor xor_1 (out_5, in_3, meiasoma_1_out_3);
  or or_1 (out_4, and_1_out, meiasoma_1_out_4);
endmodule

module Exemplo0021 (
  input  [2:0] in_1,
  input  [2:0] in_2,
  output [3:0] out_3
);

  wire meiasoma_1_out_3, vaium_1_out_4;

  MeiaSoma meiasoma_1 (.in_1(in_1[0]), .in_2(in_2[0]), .out_3(meiasoma_1_out_3), .out_4(out_3[0]));
  VaiUM vaium_1 (.in_1(meiasoma_1_out_3), .in_2(in_2[1]), .in_3(in_1[1]), .out_4(vaium_1_out_4), .out_5(out_3[1]));
  VaiUM vaium_2 (.in_1(vaium_1_out_4), .in_2(in_1[2]), .in_3(in_2[2]), .out_4(out_3[3]), .out_5(out_3[2]));

  // Notes on the sheet:
  //   Utiliza dois circuitos de meia soma e um circuito de soma vai um, para fazer soma de bit(2 entradas de 3 bits)
endmodule

module FullAdder (
  input  in_1,
  input  in_2,
  input  in_3,
  output out_4,
  output out_5
);

  wire and_1_out, xor_1_out, xor_2_out;

  xor xor_1 (xor_1_out, in_2, in_1);
  xor xor_2 (xor_2_out, in_1, in_2);
  and and_1 (and_1_out, in_3, in_3);
  xor xor_3 (out_4, in_3, xor_1_out);
  xor xor_4 (out_5, and_1_out, xor_2_out);

  // Notes on the sheet:
  //   FullAdder
endmodule
