// Logisim project Exemplo0024 e Exemplo0025.circ as structural Verilog: 2 circuits, main circuit ComparadorDeDiferençaVaiUM
module \ComparadorDeDiferençaVaiUM  (
);

  \ComparadorDeDiferença  \comparadordediferença_1  ();  // open: a, out_3, in_2
endmodule

module \ComparadorDeDiferença  (
  input  [3:0] a,
  input  [3:0] in_2,
  output [3:0] out_3
);

  xor _4 (out_3[3], a[3], in_2[3]);
  xor _3 (out_3[2], a[2], in_2[2]);
  xor _2 (out_3[1], a[1], in_2[1]);
  xor _1 (out_3[0], a[0], in_2[0]);

  // Notes on the sheet:
  //   Comparador de diferença
endmodule
