// Logisim project exemplo0023.circ as structural Verilog: 3 circuits, main circuit MeioSubtrator
module MeioSubtrator (
  input  in_1,
  input  in_2,
  output out_3,
  output out_4
);

  wire not_1_out;

  not not_1 (not_1_out, in_1);
  xor xor_1 (out_3, in_1, in_2);
  and and_1 (out_4, not_1_out, in_2);
endmodule

module Subtrator (
  input  in_1,
  input  in_2,
  input  in_3,
  output out_4
);

  wire and_1_out, and_2_out, and_3_out, not_1_out, not_2_out, xor_1_out, xor_2_out;

  not not_1 (not_1_out, in_2);
  xor xor_1 (xor_1_out, in_2, in_3);
  and and_1 (and_1_out, not_1_out, in_3);
  xor xor_2 (xor_2_out, in_1, xor_1_out);
  not not_2 (not_2_out, xor_1_out);
  and and_2 (and_2_out, not_2_out, in_1);
  and and_3 (and_3_out, and_2_out, and_1_out);
  xor xor_3 (out_4, xor_2_out, and_3_out);

  // Notes on the sheet:
  //   Utiliza dois conjuntos MeioSubtrator e uma porta AND para fazer subtração de Bits. No fim a porta XOR compara se o BIT é igual ou diferente
endmodule

module Teste (
  input  in_1,
  input  in_2,
  input  in_3,
  input  in_4,
  input  in_5,
  input  in_6,
  input  in_7,
  input  in_8,
  output out_9,
  output out_10,
  output out_11,
  output out_12
);

  nand nand_1 (out_9, in_1, in_2);
  xor xor_1 (out_10, in_3, in_4);
  xnor xnor_1 (out_11, in_5, in_6);
  nor nor_1 (out_12, in_7, in_8);

  // Notes on the sheet:
  //   Porta NAND
  //   Porta XOR
  //   Porta XNOR
  //   Porta NOR
endmodule
