// Logisim project Exemplo021.circ as structural Verilog: 4 circuits, main circuit Somador
module Somador (
  input  in_1,
  input  a,
  input  b,
  input  in_4,
  input  in_5,
  input  in_6,
  input  entrada_overflow,
  output \output ,
  output output_2,
  output output_3,
  output sinal
);

  wire and_1_out, and_2_out, and_3_out, and_4_out, and_5_out, and_6_out, or_1_out, or_2_out, xor_1_out,
       xor_2_out, xor_3_out;

  xor xor_1 (xor_1_out, b, in_6);
  and and_1 (and_1_out, b, in_6);
  xor xor_2 (xor_2_out, a, in_5);
  and and_2 (and_2_out, a, in_5);
  xor xor_3 (xor_3_out, in_1, in_4);
  and and_3 (and_3_out, in_1, in_4);
  xor xor_4 (\output , xor_1_out, entrada_overflow);
  and and_4 (and_4_out, xor_1_out, entrada_overflow);
  xor xor_5 (output_2, xor_2_out, or_1_out);
  and and_5 (and_5_out, xor_2_out, or_1_out);
  xor xor_6 (output_3, xor_3_out, or_2_out);
  and and_6 (and_6_out, xor_3_out, or_2_out);
  or or_1 (or_1_out, and_4_out, and_1_out);
  or or_2 (or_2_out, and_5_out, and_2_out);
  or or_3 (sinal, and_6_out, and_3_out);

  // Notes on the sheet:
  //   SOMADOR ENTRADA 2bit + sinal
endmodule

module NOVo (
  input  in_1,
  input  in_2,
  input  in_3,
  input  in_4,
  input  in_5,
  input  in_6,
  input  in_7,
  input  in_8,
  input  in_9,
  input  in_10,
  input  in_11,
  input  in_12,
  input  in_13,
  input  in_14,
  input  entrada_overflow,
  output output_overflow,
  output out_17,
  output out_18,
  output out_19,
  output out_20,
  output out_21,
  output out_22,
  output out_23
);

  wire somador_5_sinal, somador_6_sinal;

  Somador somador_1 (
    .entrada_overflow(entrada_overflow), .\output (in_7), .output_2(in_14), .output_3(out_23), .sinal(out_23));  // open: in_1, a, b, in_4, in_5, in_6
  Somador somador_2 (
    .entrada_overflow(out_23), .in_5(out_23), .\output (in_6), .output_2(in_13), .output_3(out_17),
    .sinal(out_17));  // open: in_1, a, b, in_4, in_6
  Somador somador_3 (
    .entrada_overflow(out_17), .b(out_17), .in_4(out_18), .in_5(out_17), .\output (in_5), .output_2(in_12),
    .output_3(out_20), .sinal(out_20));  // open: in_1, a, in_6
  Somador somador_4 (
    .entrada_overflow(out_20), .in_1(out_20), .\output (in_4), .output_2(in_11), .output_3(out_20),
    .sinal(out_19));  // open: a, b, in_4, in_5, in_6
  Somador somador_5 (
    .entrada_overflow(out_19), .\output (in_3), .output_2(in_10), .output_3(out_19), .sinal(somador_5_sinal));  // open: in_1, a, b, in_4, in_5, in_6
  Somador somador_6 (
    .entrada_overflow(somador_5_sinal), .\output (in_2), .output_2(in_9), .output_3(out_18),
    .sinal(somador_6_sinal));  // open: in_1, a, b, in_4, in_5, in_6
  Somador somador_7 (
    .entrada_overflow(somador_6_sinal), .\output (in_1), .output_2(in_8), .output_3(out_17),
    .sinal(output_overflow));  // open: in_1, a, b, in_4, in_5, in_6

  assign out_21 = out_20;
  assign out_22 = out_17;
endmodule

module novo2 (
  input  in_1,
  input  in_2,
  input  in_3,
  input  in_4,
  input  in_5,
  input  in_6,
  input  in_7,
  input  in_8,
  input  in_9,
  input  in_10,
  input  in_11,
  input  in_12,
  input  in_13,
  input  in_14,
  input  in_15,
  input  in_16,
  input  in_17,
  input  in_18,
  input  in_19,
  input  in_20,
  input  in_21,
  input  in_22,
  input  in_23,
  input  in_24,
  input  in_25,
  input  in_26,
  input  in_27,
  input  in_28,
  input  in_29,
  output out_30,
  output out_31,
  output out_32,
  output out_33,
  output out_34,
  output out_35,
  output out_36,
  output out_37,
  output out_38,
  output out_39,
  output out_40,
  output out_41,
  output out_42,
  output out_43,
  output out_44
);

  wire novo_1_output_overflow;

  NOVo novo_1 (
    .entrada_overflow(in_29), .in_1(in_8), .in_2(in_9), .in_3(in_10), .in_4(in_11), .in_5(in_12),
    .in_6(in_13), .in_7(in_14), .in_8(in_22), .in_9(in_23), .in_10(in_24), .in_11(in_25), .in_12(in_26),
    .in_13(in_27), .in_14(in_28), .output_overflow(novo_1_output_overflow), .out_17(out_38), .out_18(out_39),
    .out_19(out_40), .out_20(out_41), .out_21(out_42), .out_22(out_43), .out_23(out_44));
  NOVo novo_2 (
    .entrada_overflow(novo_1_output_overflow), .in_1(in_1), .in_2(in_2), .in_3(in_3), .in_4(in_4),
    .in_5(in_5), .in_6(in_6), .in_7(in_7), .in_8(in_15), .in_9(in_16), .in_10(in_17), .in_11(in_18),
    .in_12(in_19), .in_13(in_20), .in_14(in_21), .output_overflow(out_30), .out_17(out_31), .out_18(out_32),
    .out_19(out_33), .out_20(out_34), .out_21(out_35), .out_22(out_36), .out_23(out_37));
endmodule

module UA (
  input  A,
  input  in_2,
  input  in_3,
  input  B,
  input  in_5,
  input  in_6,
  input  in_7,
  output out_8,
  output out_9,
  output out_10,
  output out_11
);

  // Somador somador_1: pin names not known; wires that end beside it: in_7, in_3, in_6, out_11, out_11
  Somador somador_2 (
    .a(out_11), .\output (in_2), .output_2(in_5), .output_3(out_9), .sinal(out_9));  // open: entrada_overflow, in_1, b, in_4, in_5, in_6
  Somador somador_3 (
    .in_1(out_9), .b(out_9), .\output (A), .output_2(B), .output_3(out_8), .sinal(out_8));  // open: entrada_overflow, a, in_4, in_5, in_6

  assign out_10 = out_8;

  // Notes on the sheet:
  //                              SOMADORES DE 1 BIT CADA
endmodule
