// Logisim project Exemplo023.circ as structural Verilog: 1 circuit, main circuit main
module main (
  input  SINAL_de_A,
  input  A1,
  input  A2,
  input  SINAL_de_B,
  input  B1,
  input  B2,
  output S
);

  wire and_1_out, and_2_out, and_3_out, and_4_out, and_5_out, and_6_out, not_1_out, not_2_out, not_3_out,
       not_4_out, not_5_out, not_6_out;

  not not_1 (not_1_out, A2);
  not not_2 (not_2_out, A1);
  not not_3 (not_3_out, SINAL_de_A);
  not not_4 (not_4_out, B2);
  not not_5 (not_5_out, B1);
  not not_6 (not_6_out, SINAL_de_B);
  and and_1 (and_1_out, not_1_out, B2);
  and and_2 (and_2_out, not_2_out, B1);
  and and_3 (and_3_out, not_3_out, SINAL_de_B);
  and and_4 (and_4_out, A2, not_4_out);
  and and_5 (and_5_out, A1, not_5_out);
  and and_6 (and_6_out, SINAL_de_A, not_6_out);
  or or_1 (S, and_1_out, and_2_out, and_3_out, and_4_out, and_5_out, and_6_out);

  // Notes on the sheet:
  //   Fernandos Santos Silva - 414506
  //    0-IGUAl 1-DIFERENTE
endmodule
