// Logisim project Exemplo0024.circ as structural Verilog: 3 circuits, main circuit Exemplo0024
module Exemplo0024 (
  input  [2:0] a,
  input  [2:0] b,
  output S
);

  Diferenca2 diferenca2_1 (.a(a), .b(b), .S(S));

  // Notes on the sheet:
  //   Exemplo0024 - Ana Cristina - 427385
endmodule

// =!
module Diferenca (
  input  a,
  input  b,
  output s
);

  xor XOR (s, a, b);

  // Notes on the sheet:
  //   Diferença
endmodule

// =!2
module Diferenca2 (
  input  [2:0] a,
  input  [2:0] b,
  output S
);

  wire diferenca_1_s, diferenca_2_s, diferenca_3_s;

  Diferenca diferenca_1 (.a(a[0]), .b(b[0]), .s(diferenca_1_s));
  Diferenca diferenca_2 (.a(a[1]), .b(b[1]), .s(diferenca_2_s));
  Diferenca diferenca_3 (.a(a[2]), .b(b[2]), .s(diferenca_3_s));
  or OR (S, diferenca_1_s, diferenca_2_s, diferenca_3_s);

  // Notes on the sheet:
  //   Diferença 2
endmodule
