// Logisim project Exercicios.circ as structural Verilog
// FA
module FullAdder (
  input  a,
  input  b,
  input  c,
  output s1,
  output s0
);

  wire and_1_out, and_2_out, xor_1_out;

  xor xor_1 (xor_1_out, b, a);
  and and_1 (and_1_out, b, a);
  xor xor_2 (s1, c, xor_1_out);
  and and_2 (and_2_out, xor_1_out, c);
  or or_1 (s0, and_2_out, and_1_out);
endmodule

// HA
module HalfAdder (
  input  a,
  input  b,
  output s1,
  output s0
);

  xor xor_1 (s1, b, a);
  and and_1 (s0, b, a);
endmodule

// HS
module HalfSub (
  input  a,
  input  b,
  output s1,
  output s0
);

  xor xor_1 (s1, b, a);
  and and_1 (s0, b, ~a);  // AND_Gate
endmodule

// FS
module FullSub (
  input  c,
  input  a,
  input  b,
  output s1,
  output s0
);

  wire and_1_out, and_2_out, xor_1_out;

  xor xor_1 (xor_1_out, b, a);
  and and_1 (and_1_out, b, ~a);  // AND_Gate
  xor xor_2 (s1, c, xor_1_out);
  and and_2 (and_2_out, c, ~xor_1_out);  // AND_Gate
  or or_1 (s0, and_2_out, and_1_out);
endmodule

module Exercicio01 (
  input  [2:0] a,
  input  [2:0] b,
  output [3:0] out_3
);

  wire fulladder_1_s0, halfadder_1_s0;

  HalfAdder halfadder_1 (.s1(out_3[0]), .s0(halfadder_1_s0), .a(a[0]), .b(b[0]));
  FullAdder fulladder_1 (.s1(out_3[1]), .s0(fulladder_1_s0), .a(a[1]), .b(b[1]), .c(halfadder_1_s0));
  FullAdder fulladder_2 (.s1(out_3[2]), .s0(out_3[3]), .a(a[2]), .b(b[2]), .c(fulladder_1_s0));
endmodule

module Exercicio02 (
  input  [2:0] a,
  input  [2:0] b,
  output [3:0] out_3
);

  wire fullsub_1_s0, halfsub_1_s0;

  HalfSub halfsub_1 (.s1(out_3[0]), .s0(halfsub_1_s0), .a(a[0]), .b(b[0]));
  FullSub fullsub_1 (.c(halfsub_1_s0), .s1(out_3[1]), .s0(fullsub_1_s0), .a(a[1]), .b(b[1]));
  FullSub fullsub_2 (.c(fullsub_1_s0), .s1(out_3[2]), .s0(out_3[3]), .a(a[2]), .b(b[2]));
endmodule

// CI
module Exercicio03 (
  input  [2:0] a,
  input  [2:0] b,
  output [2:0] out_3
);

  xnor xnor_1 (out_3[0], b[0], a[0]);
  xnor xnor_2 (out_3[1], b[1], a[1]);
  xnor xnor_3 (out_3[2], a[2], b[2]);
endmodule

// CD
module Exercicio04 (
  input  [2:0] a,
  input  [2:0] b,
  output [2:0] out_3
);

  xor xor_1 (out_3[0], b[0], a[0]);
  xor xor_2 (out_3[1], b[1], a[1]);
  xor xor_3 (out_3[2], a[2], b[2]);
endmodule

module Exercicio05 (
  input  [2:0] in_1,
  output [3:0] out_2
);

  wire halfadder_1_s0, halfadder_2_s0;
  wire [2:0] not_1_out;

  assign not_1_out = ~in_1;  // NOT_Gate not_1, 3 bits wide
  HalfAdder halfadder_1 (.s1(out_2[0]), .s0(halfadder_1_s0), .a(1'b1), .b(not_1_out[0]));
  HalfAdder halfadder_2 (.s1(out_2[1]), .s0(halfadder_2_s0), .a(halfadder_1_s0), .b(not_1_out[1]));
  HalfAdder halfadder_3 (.s1(out_2[2]), .s0(out_2[3]), .a(halfadder_2_s0), .b(not_1_out[2]));
endmodule

module Exercicio06 (
  input  [2:0] x,
  input  [2:0] y,
  input  op,
  output carryOut,
  output [2:0] s
);

  wire fulladder_1_s0, fulladder_2_s0, fulladder_3_s0, xor_2_out, xor_3_out, xor_4_out;

  FullAdder fulladder_1 (.s1(s[2]), .s0(fulladder_1_s0), .a(xor_2_out), .b(x[2]), .c(fulladder_2_s0));
  xor xor_1 (carryOut, op, fulladder_1_s0);
  xor xor_2 (xor_2_out, op, y[2]);
  xor xor_3 (xor_3_out, op, y[1]);
  FullAdder fulladder_2 (.s1(s[1]), .s0(fulladder_2_s0), .a(xor_3_out), .b(x[1]), .c(fulladder_3_s0));
  xor xor_4 (xor_4_out, y[0], op);
  FullAdder fulladder_3 (.s1(s[0]), .s0(fulladder_3_s0), .a(xor_4_out), .b(x[0]), .c(op));
endmodule

module Exercicio07 (
  input  [2:0] X,
  input  [2:0] Y,
  input  OP,
  output [2:0] out_4
);

  wire [2:0] exercicio03_1_out_3, exercicio04_1_out_3;

  Exercicio03 exercicio03_1 (.a(X), .b(Y), .out_3(exercicio03_1_out_3));
  Exercicio04 exercicio04_1 (.a(X), .b(Y), .out_3(exercicio04_1_out_3));
  Multiplexer #(.width(3), .enable("false")) multiplexer_1 (
    .in0(exercicio03_1_out_3), .in1(exercicio04_1_out_3), .out(out_4), .sel(OP));

  // Notes on the sheet:
  //   0 = comparador igualdade
  //   1 = comparador diferença
endmodule
