// Logisim project Exemplo022.circ as structural Verilog: 3 circuits, main circuit Main
module Meio_Subtrator (
  input  in_1,
  input  in_2,
  output Saida,
  output Carry_out
);

  wire not_1_out;

  not not_1 (not_1_out, in_1);
  xor xor_1 (Saida, in_2, in_1);
  and and_1 (Carry_out, not_1_out, in_2);
endmodule

module Main (
  input  [2:0] in_1,
  input  [2:0] in_2,
  input  Carry_in,
  output [2:0] \Saída ,
  output Carry_out
);

  wire subtrator_1_out_5, subtrator_2_out_5;

  Subtrator subtrator_1 (
    .in_1(in_1[0]), .in_2(in_2[0]), .in_3(Carry_in), .Saida(\Saída [0]), .out_5(subtrator_1_out_5));
  Subtrator subtrator_2 (
    .in_1(in_1[1]), .in_2(in_2[1]), .in_3(subtrator_1_out_5), .Saida(\Saída [1]), .out_5(subtrator_2_out_5));
  Subtrator subtrator_3 (
    .in_1(in_1[2]), .in_2(in_2[2]), .in_3(subtrator_2_out_5), .Saida(\Saída [2]), .out_5(Carry_out));

  // Notes on the sheet:
  //   Subtrator de 3bits
endmodule

module Subtrator (
  input  in_1,
  input  in_2,
  input  in_3,
  output Saida,
  output out_5
);

  wire meio_subtrator_1_carry_out, meio_subtrator_1_saida, meio_subtrator_2_carry_out;

  Meio_Subtrator meio_subtrator_1 (
    .in_1(in_1), .in_2(in_2), .Saida(meio_subtrator_1_saida), .Carry_out(meio_subtrator_1_carry_out));
  Meio_Subtrator meio_subtrator_2 (
    .in_1(meio_subtrator_1_saida), .in_2(in_3), .Saida(Saida), .Carry_out(meio_subtrator_2_carry_out));
  or or_1 (out_5, meio_subtrator_1_carry_out, meio_subtrator_2_carry_out);
endmodule
