// Logisim project Exemplo024.circ as structural Verilog: 2 circuits, main circuit Comparador 3bits
module Comparador_1bit (
  input  in_1,
  input  in_2,
  output out_3
);

  xnor xnor_1 (out_3, in_1, in_2);
endmodule

module Comparador_3bits (
  input  [2:0] in_1,
  input  [2:0] in_2,
  output \Saída 
);

  wire and_1_out, comparador_1bit_1_out_3, comparador_1bit_2_out_3, comparador_1bit_3_out_3;

  Comparador_1bit comparador_1bit_1 (.in_1(in_2[1]), .in_2(in_1[1]), .out_3(comparador_1bit_1_out_3));
  Comparador_1bit comparador_1bit_2 (.in_1(in_2[0]), .in_2(in_1[0]), .out_3(comparador_1bit_2_out_3));
  and and_1 (and_1_out, comparador_1bit_2_out_3, comparador_1bit_1_out_3, comparador_1bit_3_out_3);
  not not_1 (\Saída , and_1_out);
  Comparador_1bit comparador_1bit_3 (.in_1(in_2[2]), .in_2(in_1[2]), .out_3(comparador_1bit_3_out_3));

  // Notes on the sheet:
  //   Comparador da diferença de 3 bits
endmodule
