// Logisim project Circuitos.circ as structural Verilog
// MS
module Meia_Somador (
  input  A,
  input  B,
  output S0,
  output Carry_out
);

  xor xor_1 (S0, A, B);
  and and_1 (Carry_out, A, B);

  // Notes on the sheet:
  //   Meia somador p/ 2 bits
endmodule

// SC
module Somador_completo_3_bits (
  input  C0,
  input  B0,
  input  A0,
  input  C1,
  input  B1,
  input  A1,
  output S0,
  output S1,
  output S2,
  output Carry_out
);

  wire meia_somador_1_carry_out, somador_completo_1_carry_out;

  Meia_Somador meia_somador_1 (.A(A0), .B(A1), .S0(S0), .Carry_out(meia_somador_1_carry_out));
  Somador_completo somador_completo_1 (
    .A(B0), .B(B1), .Carry_in(meia_somador_1_carry_out), .S0(S1), .Carry_out(somador_completo_1_carry_out));
  Somador_completo somador_completo_2 (
    .A(C0), .B(C1), .Carry_in(somador_completo_1_carry_out), .S0(S2), .Carry_out(Carry_out));

  // Notes on the sheet:
  //   Somador completo p/ 3 bits
endmodule

// SC
module Somador_completo (
  input  A,
  input  B,
  input  Carry_in,
  output S0,
  output Carry_out
);

  wire and_1_out, and_2_out, xor_1_out;

  xor xor_1 (xor_1_out, A, B);
  and and_1 (and_1_out, B, A);
  xor xor_2 (S0, xor_1_out, Carry_in);
  and and_2 (and_2_out, Carry_in, xor_1_out);
  or or_1 (Carry_out, and_2_out, and_1_out);

  // Notes on the sheet:
  //   Somador completo p/ 2 bits
endmodule

// C1
module Complemento_de_1 (
  input  C0,
  input  B0,
  input  A0,
  output S0,
  output S1,
  output S2
);

  not not_1 (S0, A0);
  not not_2 (S1, B0);
  not not_3 (S2, C0);

  // Notes on the sheet:
  //   Complemento de 1
  //   p/ 8 bits
endmodule

module Complemento_de_2 (
  input  C0,
  input  B0,
  input  A0,
  output S0,
  output S1,
  output S2,
  output Carry_out
);

  wire complemento_de_1_1_s0, complemento_de_1_1_s1, complemento_de_1_1_s2;

  Complemento_de_1 complemento_de_1_1 (
    .C0(C0), .B0(B0), .A0(A0), .S0(complemento_de_1_1_s0), .S1(complemento_de_1_1_s1),
    .S2(complemento_de_1_1_s2));
  Somador_completo_3_bits somador_completo_3_bits_1 (
    .C0(complemento_de_1_1_s2), .B0(complemento_de_1_1_s1), .A0(complemento_de_1_1_s0), .C1(1'b0), .B1(1'b0),
    .A1(1'b1), .S0(S0), .S1(S1), .S2(S2), .Carry_out(Carry_out));

  // Notes on the sheet:
  //   Complemento de 2
  //   p/ 4 bits
endmodule

module Meia_subtrator (
  input  A,
  input  B,
  output S0,
  output Carry_out
);

  wire not_1_out;

  not not_1 (not_1_out, A);
  xor xor_1 (S0, A, B);
  and and_1 (Carry_out, not_1_out, B);

  // Notes on the sheet:
  //   Meia subtrator p/ 2 bits
endmodule

module Subtrator_completo (
  input  A,
  input  B,
  input  Carry_in,
  output S0,
  output Carry_out
);

  wire and_1_out, xor_1_out;

  xor xor_1 (xor_1_out, B, A);
  xor xor_2 (S0, Carry_in, xor_1_out);
  and and_1 (and_1_out, xor_1_out, B);
  or or_1 (Carry_out, and_1_out, Carry_in);
endmodule

module Comparador_igualdade (
  input  C0,
  input  B0,
  input  A0,
  input  C1,
  input  B1,
  input  A1,
  output S0
);

  wire xnor_1_out, xnor_2_out, xnor_3_out;

  xnor xnor_1 (xnor_1_out, A0, A1);
  xnor xnor_2 (xnor_2_out, B0, B1);
  xnor xnor_3 (xnor_3_out, C0, C1);
  and and_1 (S0, xnor_1_out, xnor_2_out, xnor_3_out);
endmodule

module \Comparador_diferença  (
  input  C0,
  input  B0,
  input  A0,
  input  C1,
  input  B1,
  input  A1,
  output S0
);

  wire xnor_1_out, xnor_2_out, xnor_3_out;

  xnor xnor_1 (xnor_1_out, A0, A1);
  xnor xnor_2 (xnor_2_out, B0, B1);
  xnor xnor_3 (xnor_3_out, C0, C1);
  nand nand_1 (S0, xnor_1_out, xnor_2_out, xnor_3_out);
endmodule

module Comparador_de_bits_com_selecionador (
  input  C0,
  input  B0,
  input  A0,
  input  C1,
  input  B1,
  input  A1,
  input  in_7,
  output S0
);

  wire comparador_igualdade_1_s0;

  Comparador_igualdade comparador_igualdade_1 (
    .C0(C0), .B0(B0), .A0(A0), .C1(C1), .B1(B1), .A1(A1), .S0(comparador_igualdade_1_s0));
  xor xor_1 (S0, comparador_igualdade_1_s0, in_7);

  // Notes on the sheet:
  //   0 - Iguais
  //   1 - Digerentes
  //   Comparador de bits com selecionador
endmodule

module \Somador_Algébrico_selecionável__Adição_ou_Subtração  (
  input  \Adição ,
  input  \Subtração ,
  input  C0,
  input  B0,
  input  A0,
  input  C1,
  input  B1,
  input  A1,
  output S0,
  output S1,
  output S2,
  output Carry_out
);

  wire _1_out, _2_out, _3_out, _4_out, _5_out, _6_out, _9_out, _10_out, _11_out, complemento_de_1_1_s0,
       complemento_de_1_1_s1, complemento_de_1_1_s2;

  Complemento_de_1 complemento_de_1_1 (
    .C0(C1), .B0(B1), .A0(A1), .S0(complemento_de_1_1_s0), .S1(complemento_de_1_1_s1),
    .S2(complemento_de_1_1_s2));
  and _1 (_1_out, A1, \Adição );
  and _3 (_3_out, B1, \Adição );
  and _5 (_5_out, C1, \Adição );
  and _2 (_2_out, complemento_de_1_1_s0, \Subtração );
  and _4 (_4_out, complemento_de_1_1_s1, \Subtração );
  and _6 (_6_out, complemento_de_1_1_s2, \Subtração );
  or _9 (_9_out, _1_out, _2_out);
  or _10 (_10_out, _3_out, _4_out);
  or _11 (_11_out, _5_out, _6_out);
  Somador_completo_3_bits somador_completo_3_bits_1 (
    .C0(C0), .B0(B0), .A0(A0), .C1(_11_out), .B1(_10_out), .A1(_9_out), .S0(S0), .S1(S1), .S2(S2),
    .Carry_out(Carry_out));

  // Notes on the sheet:
  //   MENU
  //   P/ Adição
  //   1 - Adição
  //   0 - Subtração
  //   P/ Subtração
  //   1 - Subtração
  //   0 - Adição
endmodule

// SC
module Subtrator_completo_3_bits (
  input  C0,
  input  B0,
  input  A0,
  input  C1,
  input  B1,
  input  A1,
  output S0,
  output S1,
  output S2,
  output Carry_out
);

  wire meia_subtrator_1_carry_out, subtrator_completo_1_carry_out;

  Meia_subtrator meia_subtrator_1 (.A(A0), .B(A1), .S0(S0), .Carry_out(meia_subtrator_1_carry_out));
  Subtrator_completo subtrator_completo_1 (
    .A(B0), .B(B1), .Carry_in(meia_subtrator_1_carry_out), .S0(S1), .Carry_out(subtrator_completo_1_carry_out));
  Subtrator_completo subtrator_completo_2 (
    .A(C0), .B(C1), .Carry_in(subtrator_completo_1_carry_out), .S0(S2), .Carry_out(Carry_out));
endmodule
