// Logisim project GUIA04.circ as structural Verilog
module meia_soma (
  input  in_1,
  input  in_2,
  output out_3,
  output out_4
);

  xor xor_1 (out_3, in_2, in_1);
  and and_1 (out_4, in_2, in_1);
endmodule

module soma_vai_1 (
  input  in_1,
  input  in_2,
  input  in_3,
  output out_4,
  output out_5
);

  wire meia_soma_1_out_3, meia_soma_1_out_4, meia_soma_2_out_4;

  meia_soma meia_soma_1 (.in_1(in_2), .in_2(in_3), .out_3(meia_soma_1_out_3), .out_4(meia_soma_1_out_4));
  meia_soma meia_soma_2 (.in_1(meia_soma_1_out_3), .in_2(in_1), .out_3(out_4), .out_4(meia_soma_2_out_4));
  or or_1 (out_5, meia_soma_2_out_4, meia_soma_1_out_4);
endmodule

module Soma_3_bits (
  input  [2:0] in_1,
  input  [2:0] in_2,
  output [3:0] out_3
);

  wire meia_soma_1_out_4, soma_vai_1_1_out_5;

  meia_soma meia_soma_1 (.in_1(in_1[0]), .in_2(in_2[0]), .out_3(out_3[0]), .out_4(meia_soma_1_out_4));
  soma_vai_1 soma_vai_1_1 (
    .in_1(meia_soma_1_out_4), .in_2(in_2[1]), .in_3(in_1[1]), .out_4(out_3[1]), .out_5(soma_vai_1_1_out_5));
  soma_vai_1 soma_vai_1_2 (
    .in_1(soma_vai_1_1_out_5), .in_2(in_2[2]), .in_3(in_1[2]), .out_4(out_3[2]), .out_5(out_3[3]));
endmodule

module \Meia_diferença  (
  input  in_1,
  input  in_2,
  output out_3,
  output out_4
);

  wire not_1_out;

  not not_1 (not_1_out, in_1);
  and and_1 (out_4, not_1_out, in_2);
  xor xor_1 (out_3, in_1, in_2);
endmodule

module \Diferença_vai_1  (
  input  in_1,
  input  in_2,
  input  in_3,
  output out_4,
  output out_5
);

  wire \meia_diferença_1_out_3 , \meia_diferença_1_out_4 , \meia_diferença_2_out_4 ;

  \Meia_diferença  \meia_diferença_1  (
    .in_1(in_2), .in_2(in_1), .out_3(\meia_diferença_1_out_3 ), .out_4(\meia_diferença_1_out_4 ));
  \Meia_diferença  \meia_diferença_2  (
    .in_1(in_3), .in_2(\meia_diferença_1_out_3 ), .out_3(out_4), .out_4(\meia_diferença_2_out_4 ));
  or or_1 (out_5, \meia_diferença_2_out_4 , \meia_diferença_1_out_4 );
endmodule

module Subtrator_de_3_bits (
  input  in_1,
  input  [2:0] in_2,
  input  [2:0] in_3,
  output out_4,
  output [2:0] out_5
);

  wire \diferença_vai_1_1_out_5 , \diferença_vai_1_2_out_5 ;

  \Diferença_vai_1  \diferença_vai_1_1  (
    .in_1(in_3[0]), .in_2(in_2[0]), .in_3(in_1), .out_4(out_5[0]), .out_5(\diferença_vai_1_1_out_5 ));
  \Diferença_vai_1  \diferença_vai_1_2  (
    .in_1(in_3[1]), .in_2(in_2[1]), .in_3(\diferença_vai_1_1_out_5 ), .out_4(out_5[1]),
    .out_5(\diferença_vai_1_2_out_5 ));
  \Diferença_vai_1  \diferença_vai_1_3  (
    .in_1(in_3[2]), .in_2(in_2[2]), .in_3(\diferença_vai_1_2_out_5 ), .out_4(out_5[2]), .out_5(out_4));
endmodule

module Igualdade (
  input  [2:0] in_1,
  input  [2:0] in_2,
  output out_3
);

  wire xnor_1_out, xnor_2_out, xnor_3_out;

  xnor xnor_1 (xnor_1_out, in_2[0], in_1[0]);
  xnor xnor_2 (xnor_2_out, in_2[1], in_1[1]);
  xnor xnor_3 (xnor_3_out, in_2[2], in_1[2]);
  and and_1 (out_3, xnor_1_out, xnor_2_out, xnor_3_out);
endmodule

module \Diferença  (
  input  [2:0] in_1,
  input  [2:0] in_2,
  output out_3
);

  wire and_1_out, xnor_1_out, xnor_2_out, xnor_3_out;

  xnor xnor_1 (xnor_1_out, in_2[0], in_1[0]);
  xnor xnor_2 (xnor_2_out, in_2[1], in_1[1]);
  xnor xnor_3 (xnor_3_out, in_2[2], in_1[2]);
  not not_1 (out_3, and_1_out);
  and and_1 (and_1_out, xnor_1_out, xnor_2_out, xnor_3_out);
endmodule

module Complemento_de_2 (
  input  [2:0] in_1,
  output [3:0] out_2
);

  wire meia_soma_1_out_4, meia_soma_2_out_4, meia_soma_3_out_4;
  wire [2:0] not_1_out;

  assign not_1_out = ~in_1;  // NOT_Gate not_1, 3 bits wide
  meia_soma meia_soma_1 (.in_1(not_1_out[0]), .in_2(1'b1), .out_3(out_2[0]), .out_4(meia_soma_1_out_4));
  meia_soma meia_soma_2 (.in_1(meia_soma_1_out_4), .in_2(not_1_out[1]), .out_3(out_2[1]), .out_4(meia_soma_2_out_4));
  meia_soma meia_soma_3 (.in_1(meia_soma_2_out_4), .in_2(not_1_out[2]), .out_3(out_2[2]), .out_4(meia_soma_3_out_4));
  not not_2 (out_2[3], meia_soma_3_out_4);
endmodule
