// Logisim project Circuitos01.circ as structural Verilog: 15 circuits, main circuit Exemplo0021
module Exemplo0021 (
  input  [2:0] a,
  input  [2:0] b,
  output carry_out,
  output [2:0] s
);

  wire somador_completo_2_carry_out, somador_completo_3_carry_out;

  // Probe on a
  somador_completo somador_completo_1 (
    .a(b[2]), .b(a[2]), .carry_in(somador_completo_2_carry_out), .s(s[2]), .carry_out(carry_out));
  somador_completo somador_completo_2 (
    .a(b[1]), .b(a[1]), .carry_in(somador_completo_3_carry_out), .s(s[1]),
    .carry_out(somador_completo_2_carry_out));
  // Probe on b
  somador_completo somador_completo_3 (
    .a(b[0]), .b(a[0]), .carry_in(1'b0), .s(s[0]), .carry_out(somador_completo_3_carry_out));
  // Probe on s

  // Notes on the sheet:
  //   Exemplo0021 - Djonatas Tulio Rodrigues Costa - 440954
endmodule

module Exemplo0022 (
  input  [2:0] a,
  input  [2:0] b,
  output borrow_out,
  output [2:0] d
);

  wire subtrator_completo_2_borrow_out, subtrator_completo_3_borrow_out;

  // Probe on a
  subtrator_completo subtrator_completo_1 (
    .a(a[2]), .b(b[2]), .borrow_in(subtrator_completo_2_borrow_out), .d(d[2]), .borrow_out(borrow_out));
  subtrator_completo subtrator_completo_2 (
    .a(a[1]), .b(b[1]), .borrow_in(subtrator_completo_3_borrow_out), .d(d[1]),
    .borrow_out(subtrator_completo_2_borrow_out));
  // Probe on d
  // Probe on b
  subtrator_completo subtrator_completo_3 (
    .a(a[0]), .b(b[0]), .borrow_in(1'b0), .d(d[0]), .borrow_out(subtrator_completo_3_borrow_out));
  // Probe on d

  // Notes on the sheet:
  //   Exemplo0022 - Djonatas Tulio Rodrigues Costa - 440954
endmodule

module Exemplo0023 (
  input  [2:0] a,
  input  [2:0] b,
  output a_b
);

  wire comparador_1_a_b, comparador_2_a_b, comparador_3_a_b;

  // Probe on a
  comparador comparador_1 (.a(b[2]), .b(a[2]), .a_b(comparador_1_a_b));
  comparador comparador_2 (.a(b[1]), .b(a[1]), .a_b(comparador_2_a_b));
  and and_1 (a_b, comparador_1_a_b, comparador_2_a_b, comparador_3_a_b);
  comparador comparador_3 (.a(b[0]), .b(a[0]), .a_b(comparador_3_a_b));
  // Probe on b

  // Notes on the sheet:
  //   Exemplo0023 - Djonatas Tulio Rodrigues Costa - 440954
endmodule

module Exemplo0024 (
  input  [2:0] a,
  input  [2:0] b,
  output a__b
);

  wire comparador1_1_a__b, comparador1_2_a__b, comparador1_3_a__b;

  // Probe on a
  comparador1 comparador1_1 (.a(b[1]), .b(a[1]), .a__b(comparador1_1_a__b));
  comparador1 comparador1_2 (.a(b[2]), .b(a[2]), .a__b(comparador1_2_a__b));
  or or_1 (a__b, comparador1_2_a__b, comparador1_1_a__b, comparador1_3_a__b);
  comparador1 comparador1_3 (.a(b[0]), .b(a[0]), .a__b(comparador1_3_a__b));
  // Probe on b

  // Notes on the sheet:
  //   Exemplo0024 - Djonatas Tulio Rodrigues Costa - 440954
endmodule

module Exemplo0025 (
  input  [2:0] a,
  output carry_out,
  output [2:0] complemento_de_2
);

  wire somador_completo_2_carry_out, somador_completo_3_carry_out;
  wire [2:0] Complemento_de_1_out_2;

  complemento1 Complemento_de_1 (.a(a), .out_2(Complemento_de_1_out_2));
  somador_completo somador_completo_1 (
    .a(1'b0), .b(Complemento_de_1_out_2[2]), .carry_in(somador_completo_3_carry_out),
    .s(complemento_de_2[2]), .carry_out(carry_out));
  somador_completo somador_completo_2 (
    .a(1'b1), .b(Complemento_de_1_out_2[0]), .carry_in(1'b0), .s(complemento_de_2[0]),
    .carry_out(somador_completo_2_carry_out));
  somador_completo somador_completo_3 (
    .a(1'b0), .b(Complemento_de_1_out_2[1]), .carry_in(somador_completo_2_carry_out),
    .s(complemento_de_2[1]), .carry_out(somador_completo_3_carry_out));

  // Notes on the sheet:
  //   Exemplo0025 - Djonatas Tulio Rodrigues Costa - 440954
endmodule

module Exemplo0026 (
  input  [2:0] a,
  input  [2:0] b,
  input  carry_in___chave,
  output out_4,
  output out_5,
  output [2:0] s
);

  wire and_1_out, somador_completo_2_carry_out, somador_completo_3_carry_out;
  wire [2:0] exemplo0025_1_complemento_de_2, switch_1_s;

  // Probe on a
  somador_completo somador_completo_1 (
    .a(a[2]), .b(switch_1_s[2]), .carry_in(somador_completo_2_carry_out), .s(s[2]), .carry_out(out_5));
  // Probe on switch_1_s
  somador_completo somador_completo_2 (
    .a(a[1]), .b(switch_1_s[1]), .carry_in(somador_completo_3_carry_out), .s(s[1]),
    .carry_out(somador_completo_2_carry_out));
  // Probe on s
  switch switch_1 (.a(b), .b(exemplo0025_1_complemento_de_2), .s(switch_1_s), .chave(carry_in___chave));
  somador_completo somador_completo_3 (
    .a(a[0]), .b(switch_1_s[0]), .carry_in(and_1_out), .s(s[0]), .carry_out(somador_completo_3_carry_out));
  Exemplo0025 exemplo0025_1 (.a(b), .carry_out(out_4), .complemento_de_2(exemplo0025_1_complemento_de_2));
  and and_1 (and_1_out, ~carry_in___chave, carry_in___chave);  // AND_Gate

  // Notes on the sheet:
  //   Exemplo0026 - Djonatas Tulio Rodrigues Costa - 440954
  //   switch
  //   complemento de 2
  //   0 - soma
  //   1 - subtração
endmodule

module Exemplo0027 (
  input  [2:0] b,
  input  [2:0] a,
  input  in_3,
  output out_4
);

  wire a__b_2_a__b, a__b_3_a__b, a__b_a__b, a_b_2_a_b, a_b_3_a_b, a_b_a_b, and_1_out, and_2_out, and_3_out,
       or_1_out;

  comparador1 a__b (.a(a[2]), .b(b[2]), .a__b(a__b_a__b));
  comparador1 a__b_2 (.a(a[1]), .b(b[1]), .a__b(a__b_2_a__b));
  comparador1 a__b_3 (.a(a[0]), .b(b[0]), .a__b(a__b_3_a__b));
  or or_1 (or_1_out, a__b_a__b, a__b_2_a__b, a__b_3_a__b);
  and and_1 (and_1_out, or_1_out, ~in_3);  // AND_Gate
  or or_2 (out_4, and_1_out, and_3_out);
  comparador a_b (.a(a[2]), .b(b[2]), .a_b(a_b_a_b));
  comparador a_b_2 (.a(a[1]), .b(b[1]), .a_b(a_b_2_a_b));
  comparador a_b_3 (.a(a[0]), .b(b[0]), .a_b(a_b_3_a_b));
  and and_2 (and_2_out, a_b_a_b, a_b_2_a_b, a_b_3_a_b);
  and and_3 (and_3_out, in_3, and_2_out);

  // Notes on the sheet:
  //   Exemplo0027 - Djonatas Tulio Rodrigues Costa - 440954
endmodule

// HA
module meia_soma (
  input  a,
  input  b,
  output s,
  output carry_out
);

  xor XOR (s, a, b);
  and AND (carry_out, b, a);
endmodule

// FA
module somador_completo (
  input  a,
  input  b,
  input  carry_in,
  output s,
  output carry_out
);

  wire meia_soma_1_carry_out, meia_soma_1_s, meia_soma_2_carry_out;

  meia_soma meia_soma_1 (.a(a), .b(b), .s(meia_soma_1_s), .carry_out(meia_soma_1_carry_out));
  meia_soma meia_soma_2 (.a(carry_in), .b(meia_soma_1_s), .s(s), .carry_out(meia_soma_2_carry_out));
  or OR (carry_out, meia_soma_2_carry_out, meia_soma_1_carry_out);
endmodule

// FS
module meio_subtrator (
  input  a,
  input  b,
  output d,
  output borrow_out
);

  xor XOR (d, a, b);
  and AND (borrow_out, b, ~a);  // AND_Gate
endmodule

// FS
module subtrator_completo (
  input  a,
  input  b,
  input  borrow_in,
  output d,
  output borrow_out
);

  wire meio_subtrator_1_borrow_out, meio_subtrator_1_d, meio_subtrator_2_borrow_out;

  meio_subtrator meio_subtrator_1 (.a(a), .b(b), .d(meio_subtrator_1_d), .borrow_out(meio_subtrator_1_borrow_out));
  meio_subtrator meio_subtrator_2 (
    .a(meio_subtrator_1_d), .b(borrow_in), .d(d), .borrow_out(meio_subtrator_2_borrow_out));
  or OR (borrow_out, meio_subtrator_2_borrow_out, meio_subtrator_1_borrow_out);
endmodule

module comparador (
  input  a,
  input  b,
  output a_b
);

  xnor xnor_1 (a_b, a, b);
endmodule

module comparador1 (
  input  a,
  input  b,
  output a__b
);

  xor xor_1 (a__b, a, b);
endmodule

module complemento1 (
  input  [2:0] a,
  output [2:0] out_2
);

  not not_1 (out_2[0], a[0]);
  not not_2 (out_2[1], a[1]);
  not not_3 (out_2[2], a[2]);
endmodule

module switch (
  input  [2:0] a,
  input  [2:0] b,
  input  chave,
  output [2:0] s
);

  wire and_1_out, and_2_out, and_3_out, and_4_out, and_5_out, and_6_out;

  and and_1 (and_1_out, chave, b[2]);
  and and_2 (and_2_out, a[2], ~chave);  // AND_Gate
  or or_1 (s[2], and_2_out, and_1_out);
  and and_3 (and_3_out, ~chave, a[1]);  // AND_Gate
  and and_4 (and_4_out, chave, b[1]);
  or or_2 (s[1], and_3_out, and_4_out);
  and and_5 (and_5_out, chave, b[0]);
  and and_6 (and_6_out, ~chave, a[0]);  // AND_Gate
  or or_3 (s[0], and_6_out, and_5_out);
endmodule
