// Logisim project Exemplo0021.circ as structural Verilog: 3 circuits, main circuit main
module main (
  input  Carry_in,
  input  a0,
  input  a1,
  input  a2,
  input  Sinal_a,
  input  b0,
  input  b1,
  input  b2,
  input  Sinal_b,
  output out_10,
  output Amplitude,
  output out_12,
  output out_13,
  output out_14
);

  wire fulladder_1_s1, fulladder_2_s1, fulladder_3_s1;

  FullAdder fulladder_1 (.a(a0), .b(b0), .in_1(Carry_in), .s1(fulladder_1_s1), .s0(out_14));
  FullAdder fulladder_2 (.a(a1), .b(b1), .in_1(fulladder_1_s1), .s1(fulladder_2_s1), .s0(out_13));
  FullAdder fulladder_3 (.a(a2), .b(b2), .in_1(fulladder_2_s1), .s1(fulladder_3_s1), .s0(out_12));
  FullAdder fulladder_4 (.a(Sinal_a), .b(Sinal_b), .in_1(fulladder_3_s1), .s1(out_10), .s0(Amplitude));

  // Notes on the sheet:
  //   FU
  //   FU
  //   FU
  //   FU
  //   Guia04 - Exemplo0021
  //   Lucas Cardoso - 441694
endmodule

module HalfAdder (
  input  a,
  input  b,
  output s0,
  output s1
);

  xor XOR (s0, a, b);
  and AND (s1, a, b);
endmodule

module FullAdder (
  input  in_1,
  input  a,
  input  b,
  output s0,
  output s1
);

  wire HA_2_s1, HA_s0, HA_s1;

  HalfAdder HA (.a(a), .b(b), .s0(HA_s0), .s1(HA_s1));
  or OR (s1, HA_s1, HA_2_s1);
  HalfAdder HA_2 (.a(HA_s0), .b(in_1), .s0(s0), .s1(HA_2_s1));
endmodule
