// Logisim project Exemplo0022.circ as structural Verilog: 3 circuits, main circuit main
module main (
  input  Carry_in,
  input  a0,
  input  a1,
  input  a2,
  input  Sinal_a,
  input  b0,
  input  b1,
  input  b2,
  input  Sinal_b,
  output out_10,
  output Amplitude,
  output out_12,
  output out_13,
  output out_14
);

  wire fulldifference_1_s1, fulldifference_2_s1, fulldifference_3_s1;

  FullDifference fulldifference_1 (.a(a0), .b(b0), .in_1(Carry_in), .s1(fulldifference_1_s1), .s0(out_14));
  FullDifference fulldifference_2 (.a(a1), .b(b1), .in_1(fulldifference_1_s1), .s1(fulldifference_2_s1), .s0(out_13));
  FullDifference fulldifference_3 (.a(a2), .b(b2), .in_1(fulldifference_2_s1), .s1(fulldifference_3_s1), .s0(out_12));
  FullDifference fulldifference_4 (.a(Sinal_a), .b(Sinal_b), .in_1(fulldifference_3_s1), .s1(out_10), .s0(Amplitude));

  // Notes on the sheet:
  //   FD
  //   FD
  //   FD
  //   FD
  //   Guia04 - Exemplo0022
  //   Lucas Cardoso - 441694
endmodule

module HalfDifference (
  input  a,
  input  b,
  output s0,
  output s1
);

  wire NOT_out;

  not NOT (NOT_out, a);
  xor XOR (s0, a, b);
  and AND (s1, NOT_out, b);
endmodule

module FullDifference (
  input  in_1,
  input  a,
  input  b,
  output s0,
  output s1
);

  wire HD_2_s1, HD_s0, HD_s1;

  HalfDifference HD (.a(a), .b(b), .s0(HD_s0), .s1(HD_s1));
  or OR (s1, HD_s1, HD_2_s1);
  HalfDifference HD_2 (.a(HD_s0), .b(in_1), .s0(s0), .s1(HD_2_s1));
endmodule
