// Logisim project Exemplo0023.circ as structural Verilog: 2 circuits, main circuit main
module main (
  input  in_1,
  input  in_2,
  input  a,
  input  in_4,
  input  in_5,
  input  in_6,
  input  b,
  input  in_8,
  output s
);

  wire equal_1_out_3, equal_2_out_3, equal_3_out_3, equal_4_out_3;

  Equal equal_1 (.a(in_1), .b(in_5), .out_3(equal_1_out_3));
  Equal equal_2 (.a(in_2), .b(in_6), .out_3(equal_2_out_3));
  Equal equal_3 (.a(a), .b(b), .out_3(equal_3_out_3));
  Equal equal_4 (.a(in_4), .b(in_8), .out_3(equal_4_out_3));
  and AND (s, equal_1_out_3, equal_2_out_3, equal_3_out_3, equal_4_out_3);

  // Notes on the sheet:
  //   Guia04 - Exemplo0023
  //   Lucas Cardoso - 441694
  //   EQ
  //   EQ
  //   EQ
  //   EQ
  //   0 - Diferente
  //   1 - Igual
endmodule

module Equal (
  input  a,
  input  b,
  output out_3
);

  xnor XNOR (out_3, a, b);

  // Notes on the sheet:
  //   0 - Diferente
  //   1  - Igual
endmodule
