// Logisim project Exemplo0024.circ as structural Verilog: 2 circuits, main circuit main
module main (
  input  in_1,
  input  in_2,
  input  a,
  input  in_4,
  input  in_5,
  input  in_6,
  input  b,
  input  in_8,
  output s
);

  wire diff_1_s, diff_2_s, diff_3_s, diff_4_s;

  Diff diff_1 (.a(in_1), .b(in_5), .s(diff_1_s));
  Diff diff_2 (.a(in_2), .b(in_6), .s(diff_2_s));
  Diff diff_3 (.a(a), .b(b), .s(diff_3_s));
  Diff diff_4 (.a(in_4), .b(in_8), .s(diff_4_s));
  or OR (s, diff_1_s, diff_2_s, diff_3_s, diff_4_s);

  // Notes on the sheet:
  //   Guia04 - Exemplo0024
  //   Lucas Cardoso - 441694
  //   DF
  //   DF
  //   DF
  //   DF
  //   0 - Igual
  //   1 - Diferente
endmodule

module Diff (
  input  a,
  input  b,
  output s
);

  xor XOR (s, a, b);

  // Notes on the sheet:
  //   0 - Igual
  //   1 - Diferente
endmodule
