// Logisim project Exemplo0021.circ as structural Verilog: 3 circuits, main circuit Adder
// A
module Adder (
  input  in_1,
  input  in_2,
  input  in_3,
  output out_4,
  output out_5
);

  wire and_1_out, and_2_out, xor_1_out;

  xor xor_1 (xor_1_out, in_1, in_2);
  xor xor_2 (out_4, xor_1_out, in_3);
  and and_1 (and_1_out, in_3, xor_1_out);
  and and_2 (and_2_out, in_2, in_1);
  or or_1 (out_5, and_1_out, and_2_out);
endmodule

module Full_Adder (
  input  in_1,
  input  in_2,
  input  in_3,
  input  in_4,
  input  in_5,
  input  in_6,
  input  in_7,
  output out_8,
  output out_9,
  output out_10,
  output out_11
);

  wire adder_1_out_5, adder_2_out_5;

  Adder adder_1 (.in_1(in_1), .in_2(in_2), .in_3(in_3), .out_4(out_8), .out_5(adder_1_out_5));
  Adder adder_2 (.in_1(in_4), .in_2(in_5), .in_3(adder_1_out_5), .out_4(out_9), .out_5(adder_2_out_5));
  Adder adder_3 (.in_1(in_6), .in_2(in_7), .in_3(adder_2_out_5), .out_4(out_10), .out_5(out_11));
endmodule

module Somador (
  input  [2:0] in_1,
  input  [2:0] in_2,
  input  in_3,
  output out_4,
  output [2:0] out_5
);

  // Probe on in_1
  // Probe on in_2
  Full_Adder full_adder_1 (
    .in_1(in_3), .in_2(in_2[0]), .in_3(in_1[0]), .in_4(in_2[1]), .in_5(in_1[1]), .in_6(in_2[2]),
    .in_7(in_1[2]), .out_8(out_5[0]), .out_9(out_5[1]), .out_10(out_5[2]), .out_11(out_4));
  // Probe on out_5
endmodule
