// Logisim project Exemplo0023.circ as structural Verilog: 1 circuit, main circuit Igualdade
module Igualdade (
  input  in_1,
  input  in_2,
  input  Liga_o_circuito,
  input  in_4,
  input  in_5,
  input  in_6,
  input  in_7,
  output out_8,
  output out_9,
  output out_10,
  output IGUALDADE
);

  wire igualdade_1_out_9, igualdade_2_out_9;

  Igualdade igualdade_1 (
    .in_2(in_1), .Liga_o_circuito(in_2), .in_4(Liga_o_circuito), .out_8(out_8), .out_9(igualdade_1_out_9));  // open: in_1, in_5, in_6, in_7, out_10, IGUALDADE
  Igualdade igualdade_2 (
    .in_2(in_4), .Liga_o_circuito(in_5), .in_4(igualdade_1_out_9), .out_8(out_9), .out_9(igualdade_2_out_9));  // open: in_1, in_5, in_6, in_7, out_10, IGUALDADE
  Igualdade igualdade_3 (
    .in_2(in_6), .Liga_o_circuito(in_7), .in_4(igualdade_2_out_9), .out_8(out_10), .out_9(IGUALDADE));  // open: in_1, in_5, in_6, in_7, out_10, IGUALDADE
endmodule
