// Logisim project Exemplo0024.circ as structural Verilog: 1 circuit, main circuit Diferenca
module Diferenca (
  input  in_1,
  input  in_2,
  input  in_3,
  input  in_4,
  input  in_5,
  input  in_6,
  output Diferente
);

  wire diferenca_1_diferente, diferenca_2_diferente, diferenca_3_diferente;

  Diferenca diferenca_1 (.in_3(in_1), .in_4(in_2), .Diferente(diferenca_1_diferente));  // open: in_1, in_2, in_5, in_6
  Diferenca diferenca_2 (.in_3(in_3), .in_4(in_4), .Diferente(diferenca_2_diferente));  // open: in_1, in_2, in_5, in_6
  Diferenca diferenca_3 (.in_3(in_5), .in_4(in_6), .Diferente(diferenca_3_diferente));  // open: in_1, in_2, in_5, in_6
  or or_1 (Diferente, diferenca_1_diferente, diferenca_2_diferente, diferenca_3_diferente);
endmodule
