// Logisim project Exemplo0027.circ as structural Verilog: 5 circuits, main circuit Igualdade
// Ig
module Igualdade (
  input  in_1,
  input  in_2,
  input  in_3,
  output out_4,
  output out_5
);

  xnor xnor_1 (out_4, in_1, in_2);
  and and_1 (out_5, in_3, out_4);
endmodule

// IG
module Igualdade2 (
  input  in_1,
  input  in_2,
  input  Liga_o_circuito,
  input  in_4,
  input  in_5,
  input  in_6,
  input  in_7,
  output out_8,
  output out_9,
  output out_10,
  output IGUALDADE
);

  wire igualdade_1_out_5, igualdade_2_out_5;

  Igualdade igualdade_1 (.in_1(in_1), .in_2(in_2), .in_3(Liga_o_circuito), .out_4(out_8), .out_5(igualdade_1_out_5));
  Igualdade igualdade_2 (.in_1(in_4), .in_2(in_5), .in_3(igualdade_1_out_5), .out_4(out_9), .out_5(igualdade_2_out_5));
  Igualdade igualdade_3 (.in_1(in_6), .in_2(in_7), .in_3(igualdade_2_out_5), .out_4(out_10), .out_5(IGUALDADE));
endmodule

// Df
module Diferenca (
  input  in_1,
  input  in_2,
  output out_3
);

  xor xor_1 (out_3, in_1, in_2);
endmodule

// DF
module Diferenca2 (
  input  in_1,
  input  in_2,
  input  in_3,
  input  in_4,
  input  in_5,
  input  in_6,
  output Diferente
);

  wire diferenca_1_out_3, diferenca_2_out_3, diferenca_3_out_3;

  Diferenca diferenca_1 (.in_1(in_1), .in_2(in_2), .out_3(diferenca_1_out_3));
  Diferenca diferenca_2 (.in_1(in_3), .in_2(in_4), .out_3(diferenca_2_out_3));
  Diferenca diferenca_3 (.in_1(in_5), .in_2(in_6), .out_3(diferenca_3_out_3));
  or or_1 (Diferente, diferenca_1_out_3, diferenca_2_out_3, diferenca_3_out_3);
endmodule

module AU (
  input  [2:0] in_1,
  input  [2:0] in_2,
  input  _0___Desigualdade,
  output out_4
);

  wire and_1_out, and_2_out, diferenca2_1_diferente, igualdade2_1_igualdade, not_1_out;

  Igualdade2 igualdade2_1 (
    .in_1(in_1[0]), .in_2(in_2[0]), .Liga_o_circuito(_0___Desigualdade), .in_4(in_1[1]), .in_5(in_2[1]),
    .in_6(in_1[2]), .in_7(in_2[2]), .IGUALDADE(igualdade2_1_igualdade));  // open: out_8, out_9, out_10
  Diferenca2 diferenca2_1 (
    .in_1(in_1[0]), .in_2(in_2[0]), .in_3(in_1[1]), .in_4(in_2[1]), .in_5(in_1[2]), .in_6(in_2[2]),
    .Diferente(diferenca2_1_diferente));
  not not_1 (not_1_out, _0___Desigualdade);
  and and_1 (and_1_out, igualdade2_1_igualdade, _0___Desigualdade);
  and and_2 (and_2_out, diferenca2_1_diferente, not_1_out);
  or or_1 (out_4, and_1_out, and_2_out);

  // Notes on the sheet:
  //   1 - Igualdade
endmodule
