// Logisim project guia4.circ as structural Verilog: 9 circuits, main circuit soma completa
// FA
module soma_completa (
  input  vai_um,
  input  x,
  input  y,
  output s0,
  output s1___vai_um
);

  wire and_1_out, and_2_out, xor_1_out;

  xor xor_1 (xor_1_out, x, y);
  and and_1 (and_1_out, y, x);
  xor xor_2 (s0, vai_um, xor_1_out);
  and and_2 (and_2_out, xor_1_out, vai_um);
  or or_1 (s1___vai_um, and_2_out, and_1_out);
endmodule

// SUB
module diferenca_completa (
  input  vem_um,
  input  X,
  input  Y,
  output S0,
  output S1
);

  wire and_1_out, and_2_out, not_1_out, not_2_out, xor_1_out;

  not not_1 (not_1_out, X);
  xor xor_1 (xor_1_out, X, Y);
  and and_1 (and_1_out, Y, not_1_out);
  not not_2 (not_2_out, xor_1_out);
  xor xor_2 (S0, vem_um, xor_1_out);
  and and_2 (and_2_out, vem_um, not_2_out);
  or or_1 (S1, and_2_out, and_1_out);
endmodule

module Exercicio1 (
  input  carry_in,
  input  x1,
  input  y1,
  input  x2,
  input  y2,
  input  x3,
  input  y3,
  output S0,
  output s1,
  output s2,
  output carry_out
);

  wire soma_completa_1_s1___vai_um, soma_completa_2_s1___vai_um;

  soma_completa soma_completa_1 (.vai_um(x1), .x(carry_in), .y(y1), .s0(S0), .s1___vai_um(soma_completa_1_s1___vai_um));
  soma_completa soma_completa_2 (
    .vai_um(soma_completa_1_s1___vai_um), .x(x2), .y(y2), .s0(s1), .s1___vai_um(soma_completa_2_s1___vai_um));
  soma_completa soma_completa_3 (
    .vai_um(soma_completa_2_s1___vai_um), .x(x3), .y(y3), .s0(s2), .s1___vai_um(carry_out));
endmodule

module Exercicio2 (
  input  in_1,
  input  x1,
  input  y1,
  input  x2,
  input  y2,
  input  x3,
  input  y3,
  output out_8,
  output out_9,
  output out_10,
  output out_11
);

  wire diferenca_completa_1_s1, diferenca_completa_2_s1;

  diferenca_completa diferenca_completa_1 (.vem_um(in_1), .X(x1), .Y(y1), .S0(out_8), .S1(diferenca_completa_1_s1));
  diferenca_completa diferenca_completa_2 (
    .vem_um(x2), .X(diferenca_completa_1_s1), .Y(y2), .S0(out_9), .S1(diferenca_completa_2_s1));
  diferenca_completa diferenca_completa_3 (.vem_um(x3), .X(diferenca_completa_2_s1), .Y(y3), .S0(out_10), .S1(out_11));
endmodule

// Ig
module Exercicio3 (
  input  [2:0] in_1,
  input  [2:0] in_2,
  output out_3
);

  wire xnor_1_out, xnor_2_out, xnor_3_out;

  xnor xnor_1 (xnor_1_out, in_1[0], in_2[0]);
  xnor xnor_2 (xnor_2_out, in_1[1], in_2[1]);
  xnor xnor_3 (xnor_3_out, in_1[2], in_2[2]);
  and and_1 (out_3, xnor_1_out, xnor_2_out, xnor_3_out);
endmodule

// Desi
module Exercicio4 (
  input  [2:0] in_1,
  input  [2:0] in_2,
  output out_3
);

  wire xor_1_out, xor_2_out, xor_3_out;

  xor xor_1 (xor_1_out, in_1[0], in_2[0]);
  xor xor_2 (xor_2_out, in_1[1], in_2[1]);
  xor xor_3 (xor_3_out, in_1[2], in_2[2]);
  or or_1 (out_3, xor_1_out, xor_2_out, xor_3_out);
endmodule

module Exercicio5 (
  input  in_1,
  input  in_2,
  input  in_3,
  input  in_4,
  input  [2:0] in_5,
  output [2:0] out_6,
  output out_7
);

  wire not_1_out, not_2_out, not_3_out;

  not not_1 (not_1_out, in_1);
  not not_2 (not_2_out, in_2);
  not not_3 (not_3_out, in_3);
  Exercicio1 exercicio1_1 (
    .x1(in_5[0]), .y1(not_3_out), .x2(in_5[1]), .y2(not_2_out), .x3(in_5[2]), .y3(not_1_out),
    .carry_in(in_4), .S0(out_6[0]), .s1(out_6[1]), .s2(out_6[2]), .carry_out(out_7));
endmodule

module Exercicio6 (
  input  [2:0] in_1,
  input  [2:0] in_2,
  input  in_3,
  output [2:0] out_4,
  output out_5
);

  wire soma_completa_1_s1___vai_um, soma_completa_2_s1___vai_um, soma_completa_3_s1___vai_um, xor_2_out,
       xor_3_out, xor_4_out;

  xor xor_1 (out_5, in_3, soma_completa_1_s1___vai_um);
  xor xor_2 (xor_2_out, in_2[2], in_3);
  soma_completa soma_completa_1 (
    .vai_um(soma_completa_2_s1___vai_um), .x(in_1[2]), .y(xor_2_out), .s0(out_4[2]),
    .s1___vai_um(soma_completa_1_s1___vai_um));
  xor xor_3 (xor_3_out, in_2[1], in_3);
  soma_completa soma_completa_2 (
    .vai_um(soma_completa_3_s1___vai_um), .x(in_1[1]), .y(xor_3_out), .s0(out_4[1]),
    .s1___vai_um(soma_completa_2_s1___vai_um));
  xor xor_4 (xor_4_out, in_2[0], in_3);
  soma_completa soma_completa_3 (
    .vai_um(in_3), .x(in_1[0]), .y(xor_4_out), .s0(out_4[0]), .s1___vai_um(soma_completa_3_s1___vai_um));
endmodule

module Exercicio7 (
  input  [2:0] in_1,
  input  [2:0] in_2,
  input  in_3,
  output out_4
);

  wire and_1_out, and_2_out, exercicio3_1_out_3, exercicio4_1_out_3, not_1_out;

  Exercicio3 exercicio3_1 (.in_1(in_1), .in_2(in_2), .out_3(exercicio3_1_out_3));
  Exercicio4 exercicio4_1 (.in_1(in_2), .in_2(in_1), .out_3(exercicio4_1_out_3));
  not not_1 (not_1_out, in_3);
  and and_1 (and_1_out, exercicio3_1_out_3, in_3);
  and and_2 (and_2_out, exercicio4_1_out_3, not_1_out);
  or or_1 (out_4, and_1_out, and_2_out);
endmodule
