// Logisim project exemplo0021.circ as structural Verilog: 3 circuits, main circuit main
module main (
  input  [2:0] in_1,
  input  [2:0] in_2,
  output [3:0] out_3
);

  wire soma_1_vai_1, soma_c_vai_1_1_sv1;

  Soma soma_1 (.S(out_3[0]), .vai_1(soma_1_vai_1), .A(in_1[0]), .B(in_2[0]));
  Soma_c__vai_1 soma_c_vai_1_1 (.Vem_1(soma_1_vai_1), .S(out_3[1]), .Sv1(soma_c_vai_1_1_sv1), .A(in_1[1]), .B(in_2[1]));
  Soma_c__vai_1 soma_c_vai_1_2 (.Vem_1(soma_c_vai_1_1_sv1), .S(out_3[2]), .Sv1(out_3[3]), .A(in_1[2]), .B(in_2[2]));

  // Notes on the sheet:
  //   Soma 
endmodule

module Soma (
  input  A,
  input  B,
  output S,
  output vai_1
);

  xor xor_1 (S, B, A);
  and and_1 (vai_1, B, A);
endmodule

module Soma_c__vai_1 (
  input  Vem_1,
  input  A,
  input  B,
  output S,
  output Sv1
);

  wire and_1_out, and_2_out, xor_1_out;

  xor xor_1 (xor_1_out, B, A);
  and and_1 (and_1_out, B, A);
  and and_2 (and_2_out, Vem_1, xor_1_out);
  xor xor_2 (S, Vem_1, xor_1_out);
  or or_1 (Sv1, and_2_out, and_1_out);

  // Notes on the sheet:
  //   s1
  //   s2
  //   s3
endmodule
