// Logisim project exemplo0022.circ as structural Verilog: 3 circuits, main circuit main
module main (
  input  [2:0] in_1,
  input  [2:0] in_2,
  output [3:0] out_3
);

  wire sub_c_vai_1_1_out_5, \subtração_1_vai_1 ;

  \Subtração  \subtração_1  (.S(out_3[0]), .vai_1(\subtração_1_vai_1 ), .in_1(in_1[0]), .in_2(in_2[0]));
  Sub_c__vai_1 sub_c_vai_1_1 (
    .Vem_1(\subtração_1_vai_1 ), .out_4(out_3[1]), .out_5(sub_c_vai_1_1_out_5), .A(in_1[1]), .B(in_2[1]));
  Sub_c__vai_1 sub_c_vai_1_2 (
    .Vem_1(sub_c_vai_1_1_out_5), .out_4(out_3[2]), .out_5(out_3[3]), .A(in_1[2]), .B(in_2[2]));

  // Notes on the sheet:
  //   Subtração
endmodule

module \Subtração  (
  input  in_1,
  input  in_2,
  output S,
  output vai_1
);

  wire not_1_out;

  not not_1 (not_1_out, in_1);
  xor xor_1 (S, in_2, in_1);
  and and_1 (vai_1, in_2, not_1_out);
endmodule

module Sub_c__vai_1 (
  input  Vem_1,
  input  A,
  input  B,
  output out_4,
  output out_5
);

  wire and_1_out, and_2_out, not_1_out, not_2_out, xor_1_out;

  not not_1 (not_1_out, A);
  xor xor_1 (xor_1_out, B, A);
  and and_1 (and_1_out, B, not_1_out);
  not not_2 (not_2_out, xor_1_out);
  and and_2 (and_2_out, Vem_1, not_2_out);
  or or_1 (out_5, and_2_out, and_1_out);
  xor xor_2 (out_4, Vem_1, xor_1_out);
endmodule
