// Logisim project exemplo0023.circ as structural Verilog: 2 circuits, main circuit main
module main (
  input  [2:0] in_1,
  input  [2:0] in_2,
  output _0_diferente
);

  Igualdade igualdade_1 (.in_1(in_1), .in_2(in_2), .out_3(_0_diferente));

  // Notes on the sheet:
  //   Igualdade
  //   1 igual
endmodule

module Igualdade (
  input  [2:0] in_1,
  input  [2:0] in_2,
  output out_3
);

  wire xnor_1_out, xnor_2_out, xnor_3_out;

  xnor xnor_1 (xnor_1_out, in_2[0], in_1[0]);
  xnor xnor_2 (xnor_2_out, in_2[1], in_1[1]);
  xnor xnor_3 (xnor_3_out, in_2[2], in_1[2]);
  and and_1 (out_3, xnor_1_out, xnor_2_out, xnor_3_out);
endmodule
