// Logisim project exemplo0024.circ as structural Verilog: 2 circuits, main circuit main
module main (
  input  [2:0] in_1,
  input  [2:0] \Diferença ,
  output _0_Igual
);

  Dif dif_1 (.in_1(in_1), .in_2(\Diferença ), .out_3(_0_Igual));

  // Notes on the sheet:
  //   1 Diferente
endmodule

module Dif (
  input  [2:0] in_1,
  input  [2:0] in_2,
  output out_3
);

  wire and_1_out, xnor_1_out, xnor_2_out, xnor_3_out;

  xnor xnor_1 (xnor_1_out, in_2[0], in_1[0]);
  xnor xnor_2 (xnor_2_out, in_2[1], in_1[1]);
  xnor xnor_3 (xnor_3_out, in_2[2], in_1[2]);
  and and_1 (and_1_out, xnor_1_out, xnor_2_out, xnor_3_out);
  not not_1 (out_3, and_1_out);
endmodule
