// Logisim project exemplo0025.circ as structural Verilog: 3 circuits, main circuit main
module main (
  input  [2:0] in_1,
  output [3:0] out_2
);

  wire c2_1_out_3, soma_1_out_4;
  wire [2:0] not_1_out;

  assign not_1_out = ~in_1;  // NOT_Gate not_1, 3 bits wide
  C2 c2_1 (.A(not_1_out[0]), .s1(out_2[0]), .out_3(c2_1_out_3));
  Soma soma_1 (.A(not_1_out[1]), .B(c2_1_out_3), .s1(out_2[1]), .out_4(soma_1_out_4));
  Soma soma_2 (.A(not_1_out[2]), .B(soma_1_out_4), .s1(out_2[2]), .out_4(out_2[3]));
endmodule

module C2 (
  input  A,
  output s1,
  output out_3
);

  xor xor_1 (s1, 1'b1, A);
  and and_1 (out_3, 1'b1, A);
endmodule

module Soma (
  input  A,
  input  B,
  output s1,
  output out_4
);

  xor xor_1 (s1, B, A);
  and and_1 (out_4, B, A);

  // Notes on the sheet:
  //   s2
endmodule
