// Logisim project exemplo0026.circ as structural Verilog: 7 circuits, main circuit main
module main (
  input  [2:0] in_1,
  input  \_1___Subtração ,
  input  [2:0] in_3,
  output [3:0] out_4
);

  wire [3:0] and_1_out, and_2_out, not_1_out, soma_completa_1_out_3, sub_completa_1_out_3;

  Sub__completa sub_completa_1 (.out_3(sub_completa_1_out_3), .in_1(in_1), .in_2(in_3));
  assign not_1_out = ~{4{\_1___Subtração }};  // NOT_Gate not_1, 4 bits wide
  Soma_completa soma_completa_1 (.out_3(soma_completa_1_out_3), .in_1(in_1), .in_2(in_3));
  assign and_1_out = {4{\_1___Subtração }} & sub_completa_1_out_3;  // AND_Gate and_1, 4 bits wide
  assign and_2_out = not_1_out & soma_completa_1_out_3;  // AND_Gate and_2, 4 bits wide
  assign out_4 = and_1_out | and_2_out;  // OR_Gate or_1, 4 bits wide

  // Notes on the sheet:
  //   0 - Soma
endmodule

module Soma (
  input  A,
  input  B,
  output S,
  output vai_1
);

  xor xor_1 (S, B, A);
  and and_1 (vai_1, B, A);
endmodule

module Soma_c__vai_1 (
  input  Vem_1,
  input  A,
  input  B,
  output S,
  output Sv1
);

  wire and_1_out, and_2_out, xor_1_out;

  xor xor_1 (xor_1_out, B, A);
  and and_1 (and_1_out, B, A);
  and and_2 (and_2_out, Vem_1, xor_1_out);
  xor xor_2 (S, Vem_1, xor_1_out);
  or or_1 (Sv1, and_2_out, and_1_out);

  // Notes on the sheet:
  //   s1
  //   s2
  //   s3
endmodule

module Soma_completa (
  input  [2:0] in_1,
  input  [2:0] in_2,
  output [3:0] out_3
);

  wire soma_1_vai_1, soma_c_vai_1_1_sv1;

  Soma soma_1 (.S(out_3[0]), .vai_1(soma_1_vai_1), .A(in_2[0]), .B(in_1[0]));
  Soma_c__vai_1 soma_c_vai_1_1 (.Vem_1(soma_1_vai_1), .S(out_3[1]), .Sv1(soma_c_vai_1_1_sv1), .A(in_2[1]), .B(in_1[1]));
  Soma_c__vai_1 soma_c_vai_1_2 (.Vem_1(soma_c_vai_1_1_sv1), .S(out_3[2]), .Sv1(out_3[3]), .A(in_2[2]), .B(in_1[2]));

  // Notes on the sheet:
  //   Soma 
endmodule

module \Subtração  (
  input  in_1,
  input  in_2,
  output S,
  output vai_1
);

  wire not_1_out;

  not not_1 (not_1_out, in_1);
  xor xor_1 (S, in_2, in_1);
  and and_1 (vai_1, in_2, not_1_out);
endmodule

module sub_c__vai_1 (
  input  Vem_1,
  input  A,
  input  B,
  output out_4,
  output out_5
);

  wire and_1_out, and_2_out, not_1_out, not_2_out, xor_1_out;

  not not_1 (not_1_out, A);
  xor xor_1 (xor_1_out, B, A);
  and and_1 (and_1_out, B, not_1_out);
  not not_2 (not_2_out, xor_1_out);
  and and_2 (and_2_out, Vem_1, not_2_out);
  or or_1 (out_5, and_2_out, and_1_out);
  xor xor_2 (out_4, Vem_1, xor_1_out);
endmodule

module Sub__completa (
  input  [2:0] in_1,
  input  [2:0] in_2,
  output [3:0] out_3
);

  wire sub_c_vai_1_1_out_5, \subtração_1_vai_1 ;

  \Subtração  \subtração_1  (.S(out_3[0]), .vai_1(\subtração_1_vai_1 ), .in_1(in_1[0]), .in_2(in_2[0]));
  sub_c__vai_1 sub_c_vai_1_1 (
    .Vem_1(\subtração_1_vai_1 ), .out_4(out_3[1]), .out_5(sub_c_vai_1_1_out_5), .A(in_2[1]), .B(in_1[1]));
  sub_c__vai_1 sub_c_vai_1_2 (
    .Vem_1(sub_c_vai_1_1_out_5), .out_4(out_3[2]), .out_5(out_3[3]), .A(in_2[2]), .B(in_1[2]));

  // Notes on the sheet:
  //   Subtração
endmodule
