// Logisim project exemplo0027.circ as structural Verilog: 3 circuits, main circuit main
module main (
  input  [2:0] in_1,
  input  [2:0] in_2,
  input  _0_Igual,
  output out_4
);

  wire and_1_out, and_2_out, diferente_1_out_3, igual_1_out_3, not_1_out;

  Diferente diferente_1 (.out_3(diferente_1_out_3), .in_1(in_1), .in_2(in_2));
  Igual igual_1 (.out_3(igual_1_out_3), .in_1(in_1), .in_2(in_2));
  not not_1 (not_1_out, _0_Igual);
  and and_1 (and_1_out, diferente_1_out_3, _0_Igual);
  and and_2 (and_2_out, igual_1_out_3, not_1_out);
  or or_1 (out_4, and_1_out, and_2_out);

  // Notes on the sheet:
  //   1 Diferente
endmodule

module Igual (
  input  [2:0] in_1,
  input  [2:0] in_2,
  output out_3
);

  wire xnor_1_out, xnor_2_out, xnor_3_out;

  xnor xnor_1 (xnor_1_out, in_2[0], in_1[0]);
  xnor xnor_2 (xnor_2_out, in_2[1], in_1[1]);
  xnor xnor_3 (xnor_3_out, in_2[2], in_1[2]);
  and and_1 (out_3, xnor_1_out, xnor_2_out, xnor_3_out);
endmodule

module Diferente (
  input  [2:0] in_1,
  input  [2:0] in_2,
  output out_3
);

  wire and_1_out, xnor_1_out, xnor_2_out, xnor_3_out;

  xnor xnor_1 (xnor_1_out, in_2[0], in_1[0]);
  xnor xnor_2 (xnor_2_out, in_2[1], in_1[1]);
  xnor xnor_3 (xnor_3_out, in_2[2], in_1[2]);
  and and_1 (and_1_out, xnor_1_out, xnor_2_out, xnor_3_out);
  not not_1 (out_3, and_1_out);
endmodule
