// Logisim project Exemplo021.circ as structural Verilog: 3 circuits, main circuit main
module main (
  input  [2:0] in_1,
  input  [2:0] in_2,
  output [3:0] out_3
);

  wire meia_soma_1_out_3, soma_vai_um_1_out_4;

  Meia_Soma meia_soma_1 (.out_3(meia_soma_1_out_3), .out_4(out_3[0]), .in_1(in_1[0]), .in_2(in_2[0]));
  Soma_Vai_Um soma_vai_um_1 (
    .in_1(in_1[1]), .in_2(in_2[1]), .in_3(meia_soma_1_out_3), .out_4(soma_vai_um_1_out_4), .out_5(out_3[1]));
  Soma_Vai_Um soma_vai_um_2 (
    .in_1(in_1[2]), .in_2(in_2[2]), .in_3(soma_vai_um_1_out_4), .out_4(out_3[3]), .out_5(out_3[2]));
endmodule

module Meia_Soma (
  input  in_1,
  input  in_2,
  output out_3,
  output out_4
);

  and and_1 (out_3, in_2, in_1);
  xor xor_1 (out_4, in_2, in_1);
endmodule

module Soma_Vai_Um (
  input  in_1,
  input  in_2,
  input  in_3,
  output out_4,
  output out_5
);

  wire and_1_out, meia_soma_1_out_3, meia_soma_1_out_4;

  Meia_Soma meia_soma_1 (.out_3(meia_soma_1_out_3), .out_4(meia_soma_1_out_4), .in_1(in_1), .in_2(in_2));
  and and_1 (and_1_out, in_3, meia_soma_1_out_4);
  xor xor_1 (out_5, in_3, meia_soma_1_out_4);
  or or_1 (out_4, and_1_out, meia_soma_1_out_3);
endmodule
