// Logisim project Exemplo025.circ as structural Verilog: 3 circuits, main circuit main
module main (
  input  [2:0] in_1,
  output [3:0] out_2
);

  wire meia_soma_com_constante_1_out_2, not_1_out, not_2_out, not_3_out, soma_comum_1_out_3;

  not not_1 (not_1_out, in_1[1]);
  not not_2 (not_2_out, in_1[2]);
  not not_3 (not_3_out, in_1[0]);
  Meia_soma_com_constante meia_soma_com_constante_1 (
    .in_1(not_3_out), .out_2(meia_soma_com_constante_1_out_2), .out_3(out_2[0]));
  soma_comum soma_comum_1 (
    .in_1(not_1_out), .in_2(meia_soma_com_constante_1_out_2), .out_3(soma_comum_1_out_3), .out_4(out_2[1]));
  soma_comum soma_comum_2 (.in_1(not_2_out), .in_2(soma_comum_1_out_3), .out_3(out_2[3]), .out_4(out_2[2]));
endmodule

module Meia_soma_com_constante (
  input  in_1,
  output out_2,
  output out_3
);

  and and_1 (out_2, 1'b1, in_1);
  xor xor_1 (out_3, 1'b1, in_1);
endmodule

module soma_comum (
  input  in_1,
  input  in_2,
  output out_3,
  output out_4
);

  and and_1 (out_3, in_2, in_1);
  xor xor_1 (out_4, in_2, in_1);
endmodule
