// Logisim project Projeto de circuito do Exemplo0021.circ as structural Verilog: 2 circuits, main circuit Exemplo0021
module Exemplo0021 (
  input  [2:0] a,
  input  [2:0] b,
  input  carry_in,
  output [2:0] Soma,
  output [2:0] Vai_um
);

  AU_01 AU_01 (.a(a), .b(b), .carry_in(carry_in), .Soma(Soma), .Vai_um(Vai_um));

  // Notes on the sheet:
  //   Matrícula: 448662
  //   Nome: Josemar Alves Caetano
endmodule

module AU_01 (
  input  [2:0] a,
  input  [2:0] b,
  input  carry_in,
  output [2:0] Soma,
  output [2:0] Vai_um
);

  wire [2:0] AND1_out, AND2_out, AND3_out, XOR1_out;

  assign XOR1_out = a ^ b;  // XOR_Gate XOR1, 3 bits wide
  assign AND1_out = {3{carry_in}} & b;  // AND_Gate AND1, 3 bits wide
  assign AND2_out = a & b;  // AND_Gate AND2, 3 bits wide
  assign AND3_out = a & {3{carry_in}};  // AND_Gate AND3, 3 bits wide
  assign Soma = XOR1_out ^ {3{carry_in}};  // XOR_Gate XOR2, 3 bits wide
  assign Vai_um = AND1_out | AND2_out | AND3_out;  // OR_Gate OR1, 3 bits wide

  // Notes on the sheet:
  //   s0
  //   d0
  //   d1
  //   d2
endmodule
