// Logisim project Projeto de circuito do Exemplo0022.circ as structural Verilog: 2 circuits, main circuit Exemplo0022
module Exemplo0022 (
  input  [2:0] a,
  input  [2:0] b,
  input  carry_in,
  output [2:0] \Subtração ,
  output [2:0] Pede___um
);

  AU_02 AU_02 (.a(a), .b(b), .carry_in(carry_in), .\Subtração (\Subtração ), .Pede___um(Pede___um));

  // Notes on the sheet:
  //   Matrícula: 448662
  //   Nome: Josemar Alves Caetano
endmodule

module AU_02 (
  input  [2:0] a,
  input  [2:0] b,
  input  carry_in,
  output [2:0] \Subtração ,
  output [2:0] Pede___um
);

  wire [2:0] AND1_2_out, AND1_3_out, AND1_out, not_1_out, not_2_out, XOR1_out;

  assign not_1_out = ~a;  // NOT_Gate not_1, 3 bits wide
  assign not_2_out = ~a;  // NOT_Gate not_2, 3 bits wide
  assign XOR1_out = a ^ b;  // XOR_Gate XOR1, 3 bits wide
  assign AND1_out = not_1_out & {3{carry_in}};  // AND_Gate AND1, 3 bits wide
  assign AND1_2_out = not_2_out & b;  // AND_Gate AND1_2, 3 bits wide
  assign AND1_3_out = b & {3{carry_in}};  // AND_Gate AND1_3, 3 bits wide
  assign Pede___um = AND1_out | AND1_2_out | AND1_3_out;  // OR_Gate OR1, 3 bits wide
  assign \Subtração  = XOR1_out ^ {3{carry_in}};  // XOR_Gate XOR2, 3 bits wide

  // Notes on the sheet:
  //   s0
  //   d0
  //   d1
  //   d2
endmodule
