// Logisim project Projeto de circuito do Exemplo0023.circ as structural Verilog: 2 circuits, main circuit Exemplo0023
module Exemplo0023 (
  input  [2:0] a,
  input  [2:0] b,
  output [2:0] Igual
);

  LU_01 LU_01 (.a(a), .b(b), .Igual(Igual));

  // Notes on the sheet:
  //   Matrícula: 448662
  //   Nome: Josemar Alves Caetano
endmodule

module LU_01 (
  input  [2:0] a,
  input  [2:0] b,
  output [2:0] Igual
);

  assign Igual = ~(a ^ b);  // XNOR_Gate xnor_1, 3 bits wide
endmodule
