// Logisim project Projeto de circuito do Exemplo0024.circ as structural Verilog: 2 circuits, main circuit Exemplo0024
module Exemplo0024 (
  input  [1:0] a,
  input  [1:0] b,
  output [1:0] Diferente
);

  LU_02 LU_02 (.a(a), .b(b), .Diferente(Diferente));

  // Notes on the sheet:
  //   Matrícula: 448662
  //   Nome: Josemar Alves Caetano
endmodule

module LU_02 (
  input  [1:0] a,
  input  [1:0] b,
  output [1:0] Diferente
);

  assign Diferente = a ^ b;  // XOR_Gate XOR1, 2 bits wide
endmodule
