// Logisim project Projeto de circuito do Exemplo0025.circ as structural Verilog: 3 circuits, main circuit Exemplo0025
module Exemplo0025 (
  input  [2:0] in_1,
  output [2:0] Complemento_de_2,
  output Overflow
);

  LU_03 LU_03 (.a(in_1), .C2(Complemento_de_2), .Overflow(Overflow));

  // Notes on the sheet:
  //   Matrícula: 448662
  //   Nome: Josemar Alves Caetano
endmodule

module LU_03 (
  input  [2:0] a,
  output [2:0] C2,
  output Overflow
);

  wire AND1_out, AND2_out, AND3_out, C1_a_0__prime, C1_a_1__prime, C1_a_2__prime, NOT1_out, XOR1_out;

  C1 C1 (.a(a), .a_2__prime(C1_a_2__prime), .a_1__prime(C1_a_1__prime), .a_0__prime(C1_a_0__prime));
  xor XOR1 (XOR1_out, C1_a_2__prime, C1_a_0__prime);
  not NOT1 (NOT1_out, C1_a_1__prime);
  not NOT2 (C2[0], C1_a_0__prime);
  and AND1 (AND1_out, XOR1_out, C1_a_1__prime);
  and AND2 (AND2_out, C1_a_2__prime, C2[0]);
  and AND3 (AND3_out, C1_a_2__prime, NOT1_out);
  or OR1 (C2[2], AND1_out, AND2_out, AND3_out);
  xor XOR2 (C2[1], C1_a_1__prime, C1_a_0__prime);
  and AND4 (Overflow, C1_a_2__prime, C1_a_1__prime, C1_a_0__prime);

  // Notes on the sheet:
  //   s0
  //   s2
  //   s1
  //   s3
  //   s4
endmodule

module C1 (
  input  [2:0] a,
  output a_2__prime,
  output a_1__prime,
  output a_0__prime
);

  not not_1 (a_2__prime, a[2]);
  not not_2 (a_1__prime, a[1]);
  not not_3 (a_0__prime, a[0]);
endmodule
