// Logisim project Projeto de circuito do Exemplo0026.circ as structural Verilog: 2 circuits, main circuit Exemplo0026
module Exemplo0026 (
  input  carryIn,
  input  a,
  input  b,
  output out_4
);

  AU_03 AU_03 (.a(a), .b(b), .carryIn(carryIn), .s(out_4));

  // Notes on the sheet:
  //   Operações: 0 - Igualdade
  //   1 - Diferença
  //   Matrícula: 448662
  //   Nome: Josemar Alves Caetano
endmodule

module AU_03 (
  input  carryIn,
  input  a,
  input  b,
  output s
);

  wire NOT1_out, XOR1_out;

  not NOT1 (NOT1_out, carryIn);
  xor XOR1 (XOR1_out, a, b);
  xor XOR2 (s, XOR1_out, NOT1_out);

  // Notes on the sheet:
  //   c_n
  //   s0
endmodule
