// Logisim project Projeto de circuito do Exemplo0027.circ as structural Verilog: 3 circuits, main circuit Exemplo0027
module Exemplo0027 (
  input  \Operação ,
  input  [2:0] a,
  input  [2:0] b,
  output [2:0] s
);

  LU_04 LU_04 (.a(a), .b(b), .\Operação (\Operação ), .s(s));

  // Notes on the sheet:
  //   Operações: 0 - Igualdade
  //   1 - Diferença
  //   Matrícula: 448662
  //   Nome: Josemar Alves Caetano
endmodule

module LU_04 (
  input  \Operação ,
  input  [2:0] a,
  input  [2:0] b,
  output [2:0] s
);

  wire [2:0] OP_out_2, XOR1_out;

  OP OP (.\Operação (\Operação ), .out_2(OP_out_2));
  assign XOR1_out = a ^ b;  // XOR_Gate XOR1, 3 bits wide
  assign s = XOR1_out ^ OP_out_2;  // XOR_Gate XOR2, 3 bits wide

  // Notes on the sheet:
  //   c_n
  //   s0
endmodule

module OP (
  input  \Operação ,
  output [2:0] out_2
);

  assign out_2 = ~{3{\Operação }};  // NOT_Gate NOT1, 3 bits wide
endmodule
