// Logisim project circ.circ as structural Verilog
module somadorCompleto (
  input  in_1,
  input  in_2,
  input  in_3,
  output out_4,
  output out_5
);

  wire and_1_out, and_2_out, xor_1_out;

  xor xor_1 (xor_1_out, in_1, in_2);
  xor xor_2 (out_4, xor_1_out, in_3);
  and and_1 (and_1_out, in_3, xor_1_out);
  and and_2 (and_2_out, in_2, in_1, in_1);
  or or_1 (out_5, and_1_out, and_2_out);
endmodule

module exemplo021 (
  input  in_1,
  input  in_2,
  input  in_3,
  input  in_4,
  input  in_5,
  input  in_6,
  input  in_7,
  output out_8,
  output out_9,
  output out_10,
  output out_11
);

  wire somadorcompleto_1_out_5, somadorcompleto_2_out_5;

  somadorCompleto somadorcompleto_1 (
    .in_1(in_7), .in_2(in_6), .in_3(in_3), .out_4(out_10), .out_5(somadorcompleto_1_out_5));
  somadorCompleto somadorcompleto_2 (
    .in_1(in_2), .in_2(in_5), .in_3(somadorcompleto_1_out_5), .out_4(out_9), .out_5(somadorcompleto_2_out_5));
  somadorCompleto somadorcompleto_3 (
    .in_1(in_1), .in_2(in_4), .in_3(somadorcompleto_2_out_5), .out_4(out_8), .out_5(out_11));
endmodule

module subitratorCompleto (
  input  in_1,
  input  in_2,
  input  in_3,
  output out_4,
  output out_5
);

  wire and_1_out, and_2_out, and_3_out, not_1_out, xor_1_out;

  not not_1 (not_1_out, in_1);
  xor xor_1 (xor_1_out, in_1, in_2);
  xor xor_2 (out_4, xor_1_out, in_3);
  and and_1 (and_1_out, not_1_out, in_2);
  and and_2 (and_2_out, not_1_out, in_3);
  and and_3 (and_3_out, in_2, in_3);
  or or_1 (out_5, and_1_out, and_2_out, and_3_out);
endmodule

module Exemplo022 (
  input  a1,
  input  b1,
  input  a2,
  input  b2,
  input  a3,
  input  b3,
  input  in_7,
  output out_8,
  output out_9,
  output out_10,
  output out_11
);

  wire subitratorcompleto_1_out_5, subitratorcompleto_2_out_5;

  subitratorCompleto subitratorcompleto_1 (
    .in_1(a1), .in_2(b1), .in_3(in_7), .out_4(out_9), .out_5(subitratorcompleto_1_out_5));
  subitratorCompleto subitratorcompleto_2 (
    .in_1(a2), .in_2(b2), .in_3(subitratorcompleto_1_out_5), .out_4(out_10),
    .out_5(subitratorcompleto_2_out_5));
  subitratorCompleto subitratorcompleto_3 (
    .in_1(a3), .in_2(b3), .in_3(subitratorcompleto_2_out_5), .out_4(out_11), .out_5(out_8));
  main main_1 ();
endmodule

module exemplo0023 (
  input  [2:0] a,
  input  [2:0] b,
  output out_3
);

  wire xnor_1_out, xnor_2_out, xnor_3_out;

  xnor xnor_1 (xnor_1_out, b[0], a[0]);
  xnor xnor_2 (xnor_2_out, b[1], a[1]);
  xnor xnor_3 (xnor_3_out, a[2], b[2]);
  and and_1 (out_3, xnor_1_out, xnor_2_out, xnor_3_out);
endmodule

module exercicio024 (
  input  [2:0] a,
  input  [2:0] b,
  output out_3
);

  wire xor_1_out, xor_2_out, xor_3_out;

  xor xor_1 (xor_1_out, b[0], a[0]);
  xor xor_2 (xor_2_out, b[1], a[1]);
  xor xor_3 (xor_3_out, a[2], b[2]);
  or or_1 (out_3, xor_1_out, xor_2_out, xor_3_out);
endmodule

module exercicio025 (
  input  [2:0] in_1,
  output out_2,
  output out_3,
  output out_4,
  output out_5
);

  complementode2 complementode2_1 (
    .in_3(in_1[2]), .in_1(in_1[1]), .in_2(in_1[0]), .out_4(out_2), .out_5(out_3), .out_6(out_4), .out_7(out_5));
endmodule

module complementode2 (
  input  in_1,
  input  in_2,
  input  in_3,
  output out_4,
  output out_5,
  output out_6,
  output out_7
);

  wire not_1_out, not_2_out, not_3_out, somadorcompleto_1_out_5, somadorcompleto_2_out_5;

  not not_1 (not_1_out, in_3);
  not not_2 (not_2_out, in_1);
  not not_3 (not_3_out, in_2);
  somadorCompleto somadorcompleto_1 (
    .in_1(1'b0), .in_2(1'b1), .in_3(not_3_out), .out_4(out_7), .out_5(somadorcompleto_1_out_5));
  somadorCompleto somadorcompleto_2 (
    .in_1(not_2_out), .in_2(1'b0), .in_3(somadorcompleto_1_out_5), .out_4(out_6),
    .out_5(somadorcompleto_2_out_5));
  somadorCompleto somadorcompleto_3 (
    .in_1(not_1_out), .in_2(1'b0), .in_3(somadorcompleto_2_out_5), .out_4(out_5), .out_5(out_4));
endmodule
