// Logisim project Exercicio05.circ as structural Verilog: 3 circuits, main circuit main
module main (
  input  [2:0] a,
  output s2,
  output s1,
  output s0,
  output carry_out
);

  wire halfadder2_1_s1, halfadder_1_s1;
  wire [2:0] not_1_out;

  assign not_1_out = ~a;  // NOT_Gate not_1, 3 bits wide
  HalfAdder halfadder_1 (.a(not_1_out[0]), .s0(s0), .s1(halfadder_1_s1));
  HalfAdder2 halfadder2_1 (.a(not_1_out[1]), .b(halfadder_1_s1), .s0(s1), .s1(halfadder2_1_s1));
  HalfAdder2 halfadder2_2 (.a(not_1_out[2]), .b(halfadder2_1_s1), .s0(s2), .s1(carry_out));
endmodule

module HalfAdder (
  input  a,
  output s0,
  output s1
);

  xor xor_1 (s0, a, 1'b1);
  and and_1 (s1, a, 1'b1);
endmodule

module HalfAdder2 (
  input  a,
  input  b,
  output s0,
  output s1
);

  xor xor_1 (s0, a, b);
  and and_1 (s1, a, b);
endmodule
