// Logisim project FA.circ as structural Verilog: 2 circuits, main circuit main
module main (
  input  [2:0] in_1,
  input  in_2,
  input  [2:0] in_3,
  input  [2:0] in_4,
  output out_5
);

  wire fa_1_s2, fa_2_s2, fa_3_s2, xor_2_out, xor_3_out, xor_4_out;

  xor xor_1 (out_5, in_2, fa_1_s2);
  xor xor_2 (xor_2_out, in_3[2], in_2);
  FA fa_1 (.a(in_1[2]), .b(xor_2_out), .c(fa_2_s2), .s1(in_4[2]), .s2(fa_1_s2));
  xor xor_3 (xor_3_out, in_2, in_3[1]);
  FA fa_2 (.a(in_1[1]), .b(xor_3_out), .c(fa_3_s2), .s1(in_4[1]), .s2(fa_2_s2));
  xor xor_4 (xor_4_out, in_3[0], in_2);
  FA fa_3 (.a(in_1[0]), .b(xor_4_out), .c(in_2), .s1(in_4[0]), .s2(fa_3_s2));
endmodule

module FA (
  input  a,
  input  b,
  input  c,
  output s1,
  output s2
);

  wire AND1_out, AND2_out, AND3_out, XNOR1_out;

  xor XNOR1 (XNOR1_out, b, a);
  buf AND1 (AND1_out, b);  // AND_Gate
  and AND2 (AND2_out, a, c);
  and AND3 (AND3_out, b, a);
  xor XNOR2 (s1, XNOR1_out, c);
  or OR (s2, AND1_out, AND2_out, AND3_out);
endmodule
