// Logisim project Circuitos.circ as structural Verilog: 8 circuits, main circuit main
module main (
  input  x,
  input  y,
  output c,
  output s
);

  and and_1 (c, x, y);
  xor xor_1 (s, y, x);

  // Notes on the sheet:
  //   Aluno: Isabel Bicalho Amaro
  //   Matrícula: 451580
endmodule

// FA
module Full_Adder (
  input  x,
  input  y,
  input  c1,
  output Next_Carry,
  output s
);

  wire and1_out, and2_out, xor1_out;

  and and1 (and1_out, y, x);
  or or1 (Next_Carry, and1_out, and2_out);
  xor xor1 (xor1_out, x, y);
  xor xor2 (s, xor1_out, c1);
  and and2 (and2_out, xor1_out, c1);

  // Notes on the sheet:
  //   y
  //   x
  //   s2
  //   s1
  //   s2
  //   Next Carry
  //   y
  //   x
  //   s1
  //   c1
  //   s3
  //   c1
endmodule

module Exercicio1 (
  input  [2:0] x,
  input  [2:0] y,
  input  First_Carry,
  output Final_Carry,
  output [2:0] s
);

  wire full_adder_2_next_carry, full_adder_3_next_carry;

  Full_Adder full_adder_1 (.Next_Carry(Final_Carry), .x(x[2]), .y(y[2]), .s(s[2]), .c1(full_adder_2_next_carry));
  Full_Adder full_adder_2 (
    .Next_Carry(full_adder_2_next_carry), .x(x[1]), .y(y[1]), .s(s[1]), .c1(full_adder_3_next_carry));
  Full_Adder full_adder_3 (.Next_Carry(full_adder_3_next_carry), .x(x[0]), .y(y[0]), .s(s[0]), .c1(First_Carry));
endmodule

module Exercicio2 (
  input  [2:0] x,
  input  [2:0] y,
  output Final_Carry,
  output [2:0] s
);

  wire full_adder_2_next_carry, full_adder_3_next_carry, not1_out, not2_out, not3_out;

  not not3 (not3_out, y[2]);
  Full_Adder full_adder_1 (.Next_Carry(Final_Carry), .x(x[2]), .y(not3_out), .s(s[2]), .c1(full_adder_2_next_carry));
  not not2 (not2_out, y[1]);
  Full_Adder full_adder_2 (
    .Next_Carry(full_adder_2_next_carry), .x(x[1]), .y(not2_out), .s(s[1]), .c1(full_adder_3_next_carry));
  not not1 (not1_out, y[0]);
  Full_Adder full_adder_3 (.Next_Carry(full_adder_3_next_carry), .x(x[0]), .y(not1_out), .s(s[0]), .c1(1'b1));

  // Notes on the sheet:
  //   First Carry
  //   Subtrair 2 conjuntos de bits
  //   o complemento de 2
  //   Obs: First Carry deve ser = 1 para calcular
endmodule

module Exercicio3 (
  input  [2:0] x,
  input  [2:0] y,
  output Final_Carry,
  output resposta,
  output [2:0] s
);

  wire full_adder_2_next_carry, full_adder_3_next_carry, not1_out, not2_out, not3_out;

  not not3 (not3_out, y[2]);
  Full_Adder full_adder_1 (.Next_Carry(Final_Carry), .x(x[2]), .y(not3_out), .s(s[2]), .c1(full_adder_2_next_carry));
  not not2 (not2_out, y[1]);
  Full_Adder full_adder_2 (
    .Next_Carry(full_adder_2_next_carry), .x(x[1]), .y(not2_out), .s(s[1]), .c1(full_adder_3_next_carry));
  not not1 (not1_out, y[0]);
  Full_Adder full_adder_3 (.Next_Carry(full_adder_3_next_carry), .x(x[0]), .y(not1_out), .s(s[0]), .c1(1'b1));
  nor nor_1 (resposta, s[0], s[1], s[2]);

  // Notes on the sheet:
  //   s1
  //   s2
  //   s3
  //   First Carry
  //   3 bits de 0, eles são iguais.
  //   resposta : 0 = diferentes
  //   1 = iguais
  //   o complemento de 2
  //   Comparar de o conjunto de bits é igual ou não
  //   a partir da subtração dos 2. Se o resultado for
  //   Obs: First Carry deve ser = 1 para calcular
endmodule

module Exercicio4 (
  input  [2:0] x,
  input  [2:0] y,
  output Final_Carry,
  output resposta,
  output [2:0] s
);

  wire full_adder_2_next_carry, full_adder_3_next_carry, not1_out, not2_out, not3_out;

  not not3 (not3_out, y[2]);
  Full_Adder full_adder_1 (.Next_Carry(Final_Carry), .x(x[2]), .y(not3_out), .s(s[2]), .c1(full_adder_2_next_carry));
  not not2 (not2_out, y[1]);
  Full_Adder full_adder_2 (
    .Next_Carry(full_adder_2_next_carry), .x(x[1]), .y(not2_out), .s(s[1]), .c1(full_adder_3_next_carry));
  not not1 (not1_out, y[0]);
  Full_Adder full_adder_3 (.Next_Carry(full_adder_3_next_carry), .x(x[0]), .y(not1_out), .s(s[0]), .c1(1'b1));
  or or_1 (resposta, s[0], s[1], s[2]);

  // Notes on the sheet:
  //   s1
  //   s2
  //   s3
  //   First Carry
  //   3 bits de 0, eles são iguais.
  //   resposta : 1 = diferentes
  //   0 = iguais
  //   o complemento de 2
  //   Comparar de o conjunto de bits é igual ou não
  //   a partir da subtração dos 2. Se o resultado for
  //   Obs: First Carry deve ser = 1 para calcular
endmodule

module Exercicio5 (
  input  [2:0] x,
  output c,
  output [2:0] s
);

  wire full_adder_2_next_carry, full_adder_3_next_carry, not_1_out, not_2_out, not_3_out;

  not not_1 (not_1_out, x[2]);
  Full_Adder full_adder_1 (.Next_Carry(c), .x(1'b0), .y(not_1_out), .s(s[2]), .c1(full_adder_2_next_carry));
  Full_Adder full_adder_2 (
    .Next_Carry(full_adder_2_next_carry), .x(1'b0), .y(not_2_out), .s(s[1]), .c1(full_adder_3_next_carry));
  not not_2 (not_2_out, x[1]);
  not not_3 (not_3_out, x[0]);
  Full_Adder full_adder_3 (.Next_Carry(full_adder_3_next_carry), .x(1'b0), .y(not_3_out), .s(s[0]), .c1(1'b1));

  // Notes on the sheet:
  //   start
  //   Carry
endmodule

module Questao2_com_full_subtractor (
  input  [2:0] x,
  input  [2:0] y,
  output Final_Carry,
  output [2:0] s
);

  wire full_adder_1_next_carry, full_adder_2_next_carry, full_adder_3_next_carry, xor1_out, xor2_out,
       xor3_out;

  xor xor4 (Final_Carry, 1'b1, full_adder_1_next_carry);
  xor xor3 (xor3_out, 1'b1, y[2]);
  Full_Adder full_adder_1 (
    .Next_Carry(full_adder_1_next_carry), .x(x[2]), .y(xor3_out), .s(s[2]), .c1(full_adder_2_next_carry));
  xor xor2 (xor2_out, 1'b1, y[1]);
  Full_Adder full_adder_2 (
    .Next_Carry(full_adder_2_next_carry), .x(x[1]), .y(xor2_out), .s(s[1]), .c1(full_adder_3_next_carry));
  xor xor1 (xor1_out, y[0], 1'b1);
  Full_Adder full_adder_3 (.Next_Carry(full_adder_3_next_carry), .x(x[0]), .y(xor1_out), .s(s[0]), .c1(1'b1));

  // Notes on the sheet:
  //   First Carry
endmodule
