// Logisim project comparador de diferenca.circ as structural Verilog: 1 circuit, main circuit main
module main (
  input  in_1,
  input  in_2,
  input  in_3,
  output out_4
);

  wire or_1_out, xor_1_out, xor_2_out, xor_3_out;

  xor xor_1 (xor_1_out, in_3, in_2);
  xor xor_2 (xor_2_out, in_3, in_1);
  xor xor_3 (xor_3_out, in_2, in_1);
  or or_1 (or_1_out, xor_1_out, xor_2_out);
  or or_2 (out_4, or_1_out, xor_3_out);
endmodule
