// Logisim project comparador de igualdade.circ as structural Verilog: 1 circuit, main circuit main
module main (
  input  in_1,
  input  in_2,
  input  in_3,
  output out_4
);

  wire and_1_out, xnor_1_out, xnor_2_out, xnor_3_out;

  xnor xnor_1 (xnor_1_out, in_3, in_2);
  xnor xnor_2 (xnor_2_out, in_3, in_1);
  xnor xnor_3 (xnor_3_out, in_2, in_1);
  and and_1 (and_1_out, xnor_1_out, xnor_2_out);
  and and_2 (out_4, and_1_out, xnor_3_out);
endmodule
