// Logisim project complemento de 2.circ as structural Verilog: 2 circuits, main circuit main
module main (
  input  [2:0] in_1,
  input  in_2,
  input  in_3,
  output [2:0] out_4,
  output out_5
);

  wire fa_2_s1, fa_3_s1, not_1_out, not_2_out, not_3_out;

  not not_1 (not_1_out, in_1[1]);
  not not_2 (not_2_out, in_1[2]);
  not not_3 (not_3_out, in_1[0]);
  FA fa_1 (.s1(out_5), .x(not_2_out), .y(in_3), .s0(out_4[2]), .c(fa_2_s1));
  FA fa_2 (.s1(fa_2_s1), .x(not_1_out), .y(in_3), .s0(out_4[1]), .c(fa_3_s1));
  FA fa_3 (.s1(fa_3_s1), .x(not_3_out), .y(in_2), .s0(out_4[0]), .c(in_3));
endmodule

module FA (
  input  c,
  input  x,
  input  y,
  output s0,
  output s1
);

  wire and_1_out, and_2_out, and_3_out, xor_1_out;

  xor xor_1 (xor_1_out, y, x);
  and and_1 (and_1_out, y, c);
  and and_2 (and_2_out, x, c);
  and and_3 (and_3_out, y, x);
  xor xor_2 (s0, xor_1_out, c);
  or or_1 (s1, and_1_out, and_2_out, and_3_out);
endmodule
