// Logisim project somaCompleta_3bits.circ as structural Verilog: 2 circuits, main circuit main
module main (
  input  [2:0] in_1,
  input  [2:0] in_2,
  input  in_3,
  output out_4,
  output [2:0] out_5
);

  wire fa_2_s1, fa_3_s1;

  FA fa_1 (.s1(out_4), .x(in_1[2]), .y(in_2[2]), .s0(out_5[2]), .c(fa_2_s1));
  FA fa_2 (.s1(fa_2_s1), .x(in_1[1]), .y(in_2[1]), .s0(out_5[1]), .c(fa_3_s1));
  FA fa_3 (.s1(fa_3_s1), .x(in_1[0]), .y(in_2[0]), .s0(out_5[0]), .c(in_3));
endmodule

module FA (
  input  c,
  input  x,
  input  y,
  output s0,
  output s1
);

  wire and_1_out, and_2_out, and_3_out, or_1_out, xor_1_out;

  xor xor_1 (xor_1_out, y, x);
  and and_1 (and_1_out, y, c);
  and and_2 (and_2_out, x, c);
  and and_3 (and_3_out, y, x);
  xor xor_2 (s0, xor_1_out, c);
  or or_1 (or_1_out, and_1_out, and_2_out);
  or or_2 (s1, or_1_out, and_3_out);
endmodule
