// Logisim project somae SubCompleta3bits.circ as structural Verilog: 2 circuits, main circuit main
module main (
  input  [2:0] in_1,
  input  [2:0] in_2,
  input  in_3,
  output [2:0] out_4,
  output out_5
);

  wire fa_1_s1, fa_2_s1, fa_3_s1, xor_2_out, xor_3_out, xor_4_out;

  xor xor_1 (out_5, in_3, fa_1_s1);
  xor xor_2 (xor_2_out, in_3, in_2[2]);
  FA fa_1 (.s1(fa_1_s1), .x(in_1[2]), .y(xor_2_out), .s0(out_4[2]), .c(fa_2_s1));
  xor xor_3 (xor_3_out, in_3, in_2[1]);
  FA fa_2 (.s1(fa_2_s1), .x(in_1[1]), .y(xor_3_out), .s0(out_4[1]), .c(fa_3_s1));
  xor xor_4 (xor_4_out, in_2[0], in_3);
  FA fa_3 (.s1(fa_3_s1), .x(in_1[0]), .y(xor_4_out), .s0(out_4[0]), .c(in_3));

  // Notes on the sheet:
  //   0 soma
  //   1 subtrai
endmodule

module FA (
  input  c,
  input  x,
  input  y,
  output s0,
  output s1
);

  wire and_1_out, and_2_out, and_3_out, xor_1_out;

  xor xor_1 (xor_1_out, y, x);
  and and_1 (and_1_out, y, c);
  and and_2 (and_2_out, x, c);
  and and_3 (and_3_out, y, x);
  xor xor_2 (s0, xor_1_out, c);
  or or_1 (s1, and_1_out, and_2_out, and_3_out);
endmodule
