// Logisim project subtracaoCompleta_3bits.circ as structural Verilog: 2 circuits, main circuit main
module main (
  input  [2:0] in_1,
  input  [2:0] in_2,
  input  in_3,
  output out_4,
  output [2:0] out_5
);

  wire fa_2_out_5, fa_3_out_5;

  FA fa_1 (.out_5(out_4), .in_1(in_1[2]), .in_2(in_2[2]), .out_4(out_5[2]), .in_3(fa_2_out_5));
  FA fa_2 (.out_5(fa_2_out_5), .in_1(in_1[1]), .in_2(in_2[1]), .out_4(out_5[1]), .in_3(fa_3_out_5));
  FA fa_3 (.out_5(fa_3_out_5), .in_1(in_1[0]), .in_2(in_2[0]), .out_4(out_5[0]), .in_3(in_3));
endmodule

module FA (
  input  in_1,
  input  in_2,
  input  in_3,
  output out_4,
  output out_5
);

  wire and_1_out, and_2_out, not_1_out, not_2_out, xor_1_out;

  not not_1 (not_1_out, in_1);
  xor xor_1 (xor_1_out, in_2, in_1);
  and and_1 (and_1_out, not_1_out, in_2);
  not not_2 (not_2_out, xor_1_out);
  xor xor_2 (out_4, xor_1_out, in_3);
  and and_2 (and_2_out, not_2_out, in_3);
  or or_1 (out_5, and_2_out, and_1_out);
endmodule
