// Logisim project Exemplo0021.circ as structural Verilog: 1 circuit, main circuit main
module main (
  input  X2,
  input  X1,
  input  C,
  input  X0,
  input  Y1,
  input  Y2,
  input  Y0,
  output out_8,
  output out_9,
  output out_10,
  output out_11
);

  wire and_1_out, and_2_out, and_3_out, and_4_out, and_5_out, and_6_out, or_1_out, or_2_out, xor_1_out,
       xor_2_out, xor_3_out;

  xor xor_1 (xor_1_out, X0, Y0);
  and and_1 (and_1_out, X0, Y0);
  xor xor_2 (xor_2_out, X1, Y1);
  and and_2 (and_2_out, X1, Y1);
  xor xor_3 (xor_3_out, X2, Y2);
  and and_3 (and_3_out, X2, Y2);
  xor xor_4 (out_8, C, xor_1_out);
  and and_4 (and_4_out, C, xor_1_out);
  xor xor_5 (out_11, or_1_out, xor_2_out);
  and and_5 (and_5_out, or_1_out, xor_2_out);
  xor xor_6 (out_10, or_2_out, xor_3_out);
  and and_6 (and_6_out, or_2_out, xor_3_out);
  or or_1 (or_1_out, and_4_out, and_1_out);
  or or_2 (or_2_out, and_5_out, and_2_out);
  or or_3 (out_9, and_6_out, and_3_out);

  // Notes on the sheet:
  //   Rodolfo Herman 451612
endmodule
