// Logisim project Exemplo0025.circ as structural Verilog: 1 circuit, main circuit main
module main (
  input  X2,
  input  X1,
  input  X0,
  output out_4,
  output out_5,
  output out_6
);

  wire or_1_out;

  or or_1 (or_1_out, X1, X0);
  xor xor_1 (out_5, X1, X0);
  xor xor_2 (out_4, X2, or_1_out);

  assign out_6 = X0;

  // Notes on the sheet:
  //   Rodolfo Herman 451612
endmodule
