// Logisim project Exemplo0022.circ as structural Verilog: 1 circuit, main circuit main
// a
module main (
  input  a,
  input  b,
  input  Te,
  output S,
  output Ts
);

  wire and_1_out, and_2_out, and_3_out, not_1_out, xor_1_out;

  xor xor_1 (xor_1_out, a, b);
  not not_1 (not_1_out, a);
  and and_1 (and_1_out, not_1_out, b);
  and and_2 (and_2_out, not_1_out, Te);
  and and_3 (and_3_out, b, Te);
  or or_1 (Ts, and_1_out, and_2_out, and_3_out);
  xor xor_2 (S, xor_1_out, Te);

  // Notes on the sheet:
  //   Nome: Tiago Matta Machado Zaidan
  //   Matricula: 451620
  //   Exemplo0022
endmodule
