// Logisim project Exemplo0024.circ as structural Verilog: 1 circuit, main circuit main
module main (
  input  in_1,
  input  in_2,
  input  in_3,
  output out_4
);

  wire and_1_out, xnor_1_out, xnor_2_out, xnor_3_out;

  xnor xnor_1 (xnor_1_out, in_1, in_2);
  xnor xnor_2 (xnor_2_out, in_3, in_1);
  xnor xnor_3 (xnor_3_out, in_3, in_2);
  not not_1 (out_4, and_1_out);
  and and_1 (and_1_out, xnor_1_out, xnor_2_out, xnor_3_out);

  // Notes on the sheet:
  //   Nome: Tiago Matta Machado Zaidan
  //   Matricula: 451620
  //   Exemplo0024
  //   saida 1 = diferentes
  //   saida 0 = iguais
endmodule
