// Logisim project Exemplo0025.circ as structural Verilog: 1 circuit, main circuit main
module main (
  input  [2:0] in_1,
  output [2:0] out_2
);

  wire and_1_out, and_2_out, not_1_out, not_2_out, xor_1_out;

  not not_1 (not_1_out, in_1[2]);
  not not_2 (not_2_out, in_1[0]);
  and and_1 (and_1_out, not_1_out, in_1[0]);
  xor xor_1 (xor_1_out, in_1[1], in_1[2]);
  and and_2 (and_2_out, not_2_out, xor_1_out);
  xor xor_2 (out_2[1], in_1[1], in_1[0]);
  or or_1 (out_2[2], and_1_out, and_2_out);

  assign out_2[0] = in_1[0];

  // Notes on the sheet:
  //   Nome: Tiago Matta Machado Zaidan
  //   Matricula: 451620
  //   Exemplo0025
endmodule
