// Logisim project Exemplo0027.circ as structural Verilog: 3 circuits, main circuit main
module main (
  input  in_1,
  input  in_2,
  input  in_3,
  input  in_4,
  output out_5
);

  wire and_1_out, and_2_out, dif_1_out_4, igu_1_out_4, not_1_out;

  Dif dif_1 (.in_1(in_1), .in_2(in_2), .in_3(in_3), .out_4(dif_1_out_4));
  Igu igu_1 (.in_1(in_1), .in_2(in_2), .in_3(in_3), .out_4(igu_1_out_4));
  not not_1 (not_1_out, in_4);
  and and_1 (and_1_out, not_1_out, dif_1_out_4);
  and and_2 (and_2_out, igu_1_out_4, in_4);
  or or_1 (out_5, and_1_out, and_2_out);

  // Notes on the sheet:
  //   Nome: Tiago Matta Machado Zaidan
  //   Matricula: 451620
  //   Exemplo0027
  //   chave = 0 diferenca
  //   chave = 1 igualdade
endmodule

module Dif (
  input  in_1,
  input  in_2,
  input  in_3,
  output out_4
);

  wire and_1_out, xnor_1_out, xnor_2_out, xnor_3_out;

  xnor xnor_1 (xnor_1_out, in_1, in_2);
  xnor xnor_2 (xnor_2_out, in_3, in_1);
  xnor xnor_3 (xnor_3_out, in_3, in_2);
  not not_1 (out_4, and_1_out);
  and and_1 (and_1_out, xnor_1_out, xnor_2_out, xnor_3_out);

  // Notes on the sheet:
  //   saida 1 = diferentes
  //   saida 0 = iguais
endmodule

module Igu (
  input  in_1,
  input  in_2,
  input  in_3,
  output out_4
);

  wire xnor_1_out, xnor_2_out, xnor_3_out;

  xnor xnor_1 (xnor_1_out, in_1, in_2);
  xnor xnor_2 (xnor_2_out, in_3, in_1);
  xnor xnor_3 (xnor_3_out, in_3, in_2);
  and and_1 (out_4, xnor_1_out, xnor_2_out, xnor_3_out);

  // Notes on the sheet:
  //   saida 1 = diferentes
  //   saida 0 = iguais
endmodule
