// Logisim project EstudoDirigido04.circ as structural Verilog: 10 circuits, main circuit 1.Somador
// S
module _1_Somador (
  input  Cn,
  input  A,
  input  B,
  output Soma,
  output Co
);

  wire and_1_out, and_2_out, xor_1_out;

  xor xor_1 (xor_1_out, Cn, A);
  xor xor_2 (Soma, xor_1_out, B);
  and and_1 (and_1_out, xor_1_out, B);
  and and_2 (and_2_out, A, Cn);
  or or_1 (Co, and_1_out, and_2_out);

  // Notes on the sheet:
  //   Wadson Ferreira - 460631
endmodule

// S3
module _1_Somador3bits (
  input  Cn,
  input  [2:0] A,
  input  [2:0] B,
  output [2:0] S
);

  wire n1_somador_1_co, n1_somador_2_co;

  _1_Somador u_1_somador_1 (.Cn(Cn), .A(A[0]), .B(B[0]), .Soma(S[0]), .Co(n1_somador_1_co));
  _1_Somador u_1_somador_2 (.Cn(n1_somador_1_co), .A(A[1]), .B(B[1]), .Soma(S[1]), .Co(n1_somador_2_co));
  _1_Somador u_1_somador_3 (.Cn(n1_somador_2_co), .A(A[2]), .B(B[2]), .Soma(S[2]));  // open: Co

  // Notes on the sheet:
  //   Wadson Ferreira - 460631
endmodule

// Sub3
module _2a_Subtrator3bits (
  input  [2:0] A,
  input  [2:0] B,
  output [2:0] out_3
);

  wire n1_somador_1_co, n1_somador_2_co, not_1_out, not_2_out, not_3_out;

  not not_1 (not_1_out, B[0]);
  _1_Somador u_1_somador_1 (.Cn(1'b1), .A(A[0]), .B(not_1_out), .Soma(out_3[0]), .Co(n1_somador_1_co));
  not not_2 (not_2_out, B[1]);
  _1_Somador u_1_somador_2 (.Cn(n1_somador_1_co), .A(A[1]), .B(not_2_out), .Soma(out_3[1]), .Co(n1_somador_2_co));
  not not_3 (not_3_out, B[2]);
  _1_Somador u_1_somador_3 (.Cn(n1_somador_2_co), .A(A[2]), .B(not_3_out), .Soma(out_3[2]));  // open: Co

  // Notes on the sheet:
  //   Wadson Ferreira - 460631
endmodule

// Sub
module _2b_Subtrator (
  input  Cn,
  input  A,
  input  B,
  output S,
  output Co
);

  wire and_1_out, and_2_out, not_1_out, not_2_out, xor_1_out;

  not not_1 (not_1_out, A);
  xor xor_1 (xor_1_out, A, B);
  and and_1 (and_1_out, B, not_1_out);
  xor xor_2 (S, Cn, xor_1_out);
  and and_2 (and_2_out, Cn, not_2_out);
  not not_2 (not_2_out, xor_1_out);
  or or_1 (Co, and_2_out, and_1_out);

  // Notes on the sheet:
  //   Wadson Ferreira - 460631
endmodule

module _2b_Subtrator3bits (
  input  [2:0] A,
  input  [2:0] B,
  output [2:0] out_3
);

  wire n2b_subtrator_1_co, n2b_subtrator_2_co;

  _2b_Subtrator u_2b_subtrator_1 (.Cn(1'b0), .A(A[0]), .B(B[0]), .S(out_3[0]), .Co(n2b_subtrator_1_co));
  _2b_Subtrator u_2b_subtrator_2 (.Cn(n2b_subtrator_1_co), .A(A[1]), .B(B[1]), .S(out_3[1]), .Co(n2b_subtrator_2_co));
  _2b_Subtrator u_2b_subtrator_3 (.Cn(n2b_subtrator_2_co), .A(A[2]), .B(B[2]), .S(out_3[2]));  // open: Co

  // Notes on the sheet:
  //   Wadson Ferreira - 460631
endmodule

// CI
module _3_Comparador_Igualdade (
  input  [2:0] A,
  input  [2:0] B,
  output S
);

  wire xor_1_out, xor_2_out, xor_3_out;

  xor xor_1 (xor_1_out, A[0], B[0]);
  nor nor_1 (S, xor_1_out, xor_2_out, xor_3_out);
  xor xor_2 (xor_2_out, A[1], B[1]);
  xor xor_3 (xor_3_out, A[2], B[2]);

  // Notes on the sheet:
  //   Wadson Ferreira - 460631
  //   1 -> A=B
  //   0 -> A!=B
endmodule

// CD
module \_4_Comparador_Diferença  (
  input  [2:0] A,
  input  [2:0] B,
  output S
);

  wire xor_1_out, xor_2_out, xor_3_out;

  xor xor_1 (xor_1_out, A[0], B[0]);
  xor xor_2 (xor_2_out, A[1], B[1]);
  xor xor_3 (xor_3_out, A[2], B[2]);
  or or_1 (S, xor_1_out, xor_2_out, xor_3_out);

  // Notes on the sheet:
  //   Wadson Ferreira - 460631
  //   1 -> A!=B
  //   0 -> A=B
endmodule

// C2
module _5_Complemento_2 (
  input  [2:0] A,
  output [2:0] out_2
);

  wire [2:0] not_1_out;

  not not_1 (not_1_out[0], A[0]);
  not not_2 (not_1_out[1], A[1]);
  not not_3 (not_1_out[2], A[2]);
  _1_Somador3bits u_1_somador3bits_1 (.Cn(1'b1), .A(not_1_out), .B(3'b000), .S(out_2));

  // Notes on the sheet:
  //   Wadson Ferreira - 460631
endmodule

// CS
module \_6_Comparador__Subtracão  (
  input  Select,
  input  [2:0] A,
  input  [2:0] B,
  output [2:0] S
);

  wire n1_somador_1_co, n1_somador_2_co, xor_1_out, xor_2_out, xor_3_out;

  xor xor_1 (xor_1_out, Select, B[0]);
  _1_Somador u_1_somador_1 (.Cn(Select), .A(A[0]), .B(xor_1_out), .Soma(S[0]), .Co(n1_somador_1_co));
  _1_Somador u_1_somador_2 (.Cn(n1_somador_1_co), .A(A[1]), .B(xor_2_out), .Soma(S[1]), .Co(n1_somador_2_co));
  xor xor_2 (xor_2_out, A[2], B[1]);
  xor xor_3 (xor_3_out, Select, B[2]);
  _1_Somador u_1_somador_3 (.Cn(n1_somador_2_co), .A(A[2]), .B(xor_3_out), .Soma(S[2]));  // open: Co

  // Notes on the sheet:
  //   Wadson Ferreira - 460631
endmodule

// CC
module _7_Comparador_Chave (
  input  Chave,
  input  [2:0] A,
  input  [2:0] B,
  output S
);

  wire and_1_out, and_2_out, n3_comparador_igualdade_1_s, \n4_comparador_diferença_1_s , not_1_out;

  _3_Comparador_Igualdade u_3_comparador_igualdade_1 (.A(A), .B(B), .S(n3_comparador_igualdade_1_s));
  \_4_Comparador_Diferença  \u_4_comparador_diferença_1  (.A(A), .B(B), .S(\n4_comparador_diferença_1_s ));
  not not_1 (not_1_out, Chave);
  and and_1 (and_1_out, not_1_out, n3_comparador_igualdade_1_s);
  and and_2 (and_2_out, Chave, \n4_comparador_diferença_1_s );
  or or_1 (S, and_1_out, and_2_out);

  // Notes on the sheet:
  //   Wadson Ferreira - 460631
endmodule
