// Logisim project Exemplo0021.circ as structural Verilog: 1 circuit, main circuit main
module main (
  input  in_1,
  input  in_2,
  input  in_3,
  input  in_4,
  input  in_5,
  input  in_6,
  input  in_7,
  output out_8,
  output out_9,
  output out_10,
  output out_11
);

  wire and_1_out, and_2_out, and_3_out, and_4_out, and_5_out, and_6_out, or_1_out, or_2_out, xor_1_out,
       xor_2_out, xor_4_out;

  xor xor_1 (xor_1_out, in_4, in_7);
  and and_1 (and_1_out, in_7, in_4);
  xor xor_2 (xor_2_out, in_3, in_6);
  and and_2 (and_2_out, in_3, in_6);
  xor xor_3 (out_8, in_1, xor_1_out);
  and and_3 (and_3_out, in_1, xor_1_out);
  xor xor_4 (xor_4_out, in_2, in_5);
  and and_4 (and_4_out, in_2, in_5);
  or or_1 (or_1_out, and_3_out, and_1_out);
  xor xor_5 (out_11, or_1_out, xor_2_out);
  and and_5 (and_5_out, or_1_out, xor_2_out);
  or or_2 (or_2_out, and_5_out, and_2_out);
  xor xor_6 (out_10, or_2_out, xor_4_out);
  and and_6 (and_6_out, or_2_out, xor_4_out);
  or or_3 (out_9, and_6_out, and_4_out);
endmodule
