// Logisim project Exemplo0021.circ as structural Verilog: 3 circuits, main circuit soma
module soma (
  input  a,
  input  b,
  input  carryIn,
  output soma,
  output carryOut
);

  wire and_1_out, and_2_out, xor_1_out, xor_2_out;

  xor xor_1 (xor_1_out, a, b);
  xor xor_2 (xor_2_out, a, b);
  xor xor_3 (soma, xor_1_out, carryIn);
  and and_1 (and_1_out, xor_2_out, carryIn);
  and and_2 (and_2_out, a, b);
  or or_1 (carryOut, and_1_out, and_2_out);
endmodule

module soma_3_bits (
  input  [2:0] a,
  input  [2:0] b,
  input  carryIn,
  output [2:0] s,
  output carryOut
);

  wire soma_1_carryout, soma_2_carryout;

  soma soma_1 (.a(a[0]), .b(b[0]), .carryIn(carryIn), .soma(s[0]), .carryOut(soma_1_carryout));
  soma soma_2 (.a(a[1]), .b(b[1]), .carryIn(soma_1_carryout), .soma(s[1]), .carryOut(soma_2_carryout));
  soma soma_3 (.a(a[2]), .b(b[2]), .carryIn(soma_2_carryout), .soma(s[2]), .carryOut(carryOut));
endmodule

module soma_compac (
  input  [2:0] a,
  input  [2:0] b,
  input  in_3,
  output [2:0] soma,
  output carryOut
);

  soma_3_bits soma_3_bits_1 (.a(a), .b(b), .carryIn(in_3), .s(soma), .carryOut(carryOut));
endmodule
