// Logisim project Exemplo0022.circ as structural Verilog: 3 circuits, main circuit diff
module diff (
  input  a,
  input  b,
  input  carryIn,
  output diff,
  output carryOut
);

  wire and_1_out, and_2_out, not_1_out, xor_1_out, xor_3_out;

  not not_1 (not_1_out, a);
  xor xor_1 (xor_1_out, a, b);
  xor xor_2 (diff, xor_1_out, carryIn);
  xor xor_3 (xor_3_out, b, carryIn);
  and and_1 (and_1_out, xor_3_out, not_1_out);
  and and_2 (and_2_out, b, carryIn);
  or or_1 (carryOut, and_1_out, and_2_out);
endmodule

module diff_3_bits (
  input  [2:0] a,
  input  [2:0] b,
  input  in_3,
  output [2:0] diff,
  output carryOut
);

  wire diff_1_carryout, diff_2_carryout;

  diff diff_1 (.a(a[0]), .b(b[0]), .carryIn(in_3), .diff(diff[0]), .carryOut(diff_1_carryout));
  diff diff_2 (.a(a[1]), .b(b[1]), .carryIn(diff_1_carryout), .diff(diff[1]), .carryOut(diff_2_carryout));
  diff diff_3 (.a(a[2]), .b(b[2]), .carryIn(diff_2_carryout), .diff(diff[2]), .carryOut(carryOut));
endmodule

module diff_compac (
  input  [2:0] a,
  input  [2:0] b,
  input  carryIn,
  output [2:0] diff,
  output carryOut
);

  diff_3_bits diff_3_bits_1 (.a(a), .b(b), .in_3(carryIn), .diff(diff), .carryOut(carryOut));
endmodule
