// Logisim project Exemplo0023.circ as structural Verilog: 3 circuits, main circuit comparador de igualdade
module comparador_de_igualdade (
  input  a,
  input  b,
  input  c,
  output out_4
);

  wire xnor_1_out, xnor_2_out, xnor_3_out;

  xnor xnor_1 (xnor_1_out, a, b);
  xnor xnor_2 (xnor_2_out, a, c);
  xnor xnor_3 (xnor_3_out, b, c);
  and and_1 (out_4, xnor_1_out, xnor_2_out, xnor_3_out);
endmodule

module comparador_3_bits (
  input  [2:0] a,
  input  [2:0] b,
  input  in_3,
  output [2:0] out_4
);

  comparador_de_igualdade comparador_de_igualdade_1 (.a(in_3), .b(a[2]), .c(b[2]), .out_4(out_4[2]));
  comparador_de_igualdade comparador_de_igualdade_2 (.a(in_3), .b(a[1]), .c(b[1]), .out_4(out_4[1]));
  comparador_de_igualdade comparador_de_igualdade_3 (.a(in_3), .b(a[0]), .c(b[0]), .out_4(out_4[0]));
endmodule

module comparador_compac (
  input  [2:0] a,
  input  [2:0] b,
  input  in_3,
  output [2:0] out_4
);

  comparador_3_bits comparador_3_bits_1 (.in_3(in_3), .a(a), .b(b), .out_4(out_4));

  // Notes on the sheet:
  //   1   se igual
  //   0   se diferente
endmodule
