// Logisim project Exemplo0024.circ as structural Verilog: 3 circuits, main circuit comparador de diferença
module \comparador_de_diferença  (
  input  a,
  input  b,
  input  c,
  output s
);

  wire xor_1_out, xor_2_out, xor_3_out;

  xor xor_1 (xor_1_out, a, b);
  xor xor_2 (xor_2_out, a, c);
  xor xor_3 (xor_3_out, b, c);
  or or_1 (s, xor_1_out, xor_2_out, xor_3_out);
endmodule

module comparador_3_bits (
  input  [2:0] a,
  input  [2:0] b,
  input  c,
  output [2:0] out_4
);

  \comparador_de_diferença  \comparador_de_diferença_1  (.a(a[0]), .b(b[1]), .c(c), .s(out_4[0]));
  \comparador_de_diferença  \comparador_de_diferença_2  (.a(b[0]), .b(a[1]), .c(c), .s(out_4[1]));
  \comparador_de_diferença  \comparador_de_diferença_3  (.a(a[2]), .b(b[2]), .c(c), .s(out_4[2]));
endmodule

module comparador_compac (
  input  [2:0] a,
  input  [2:0] b,
  input  c,
  output [2:0] s
);

  comparador_3_bits comparador_3_bits_1 (.c(c), .a(a), .b(b), .out_4(s));
endmodule
