// Logisim project Exemplo0025.circ as structural Verilog: 2 circuits, main circuit C2
module C2 (
  input  [2:0] e,
  output [2:0] out_2,
  output carryOut
);

  wire and_1_out, and_2_out, and_3_out, and_4_out, and_5_out, not_1_out, not_2_out, not_3_out, not_4_out,
       not_5_out, not_6_out, not_7_out, not_8_out, not_9_out, xor_1_out;

  not not_1 (not_1_out, e[1]);
  not not_2 (not_2_out, e[1]);
  not not_3 (not_3_out, e[2]);
  not not_4 (not_4_out, e[2]);
  not not_5 (not_5_out, e[1]);
  not not_6 (not_6_out, e[0]);
  not not_7 (not_7_out, e[2]);
  not not_8 (not_8_out, e[1]);
  not not_9 (not_9_out, e[0]);
  and and_1 (and_1_out, e[2], not_1_out);
  xor xor_1 (xor_1_out, e[1], e[0]);
  and and_2 (and_2_out, e[2], not_2_out);
  and and_3 (and_3_out, not_3_out, e[0]);
  and and_4 (and_4_out, not_4_out, e[1]);
  and and_5 (and_5_out, not_5_out, not_6_out, e[2]);
  and and_6 (carryOut, not_7_out, not_8_out, not_9_out);
  or or_1 (out_2[0], and_1_out, e[0]);
  or or_2 (out_2[1], xor_1_out, and_2_out);
  or or_3 (out_2[2], and_3_out, and_4_out, and_5_out);
endmodule

module c2_compac (
  input  [2:0] e,
  output [2:0] c2,
  output carryOut
);

  C2 c2_1 (.e(e), .out_2(c2), .carryOut(carryOut));
endmodule
