// Logisim project Exemplo0026.circ as structural Verilog: 2 circuits, main circuit sum/diff
// AU
module sum_diff (
  input  [2:0] a,
  input  [2:0] b,
  input  carryIn,
  output [2:0] out_4,
  output soma
);

  wire soma_1_carryout, soma_2_carryout, soma_3_carryout, xor_1_out, xor_2_out, xor_3_out;

  xor xor_1 (xor_1_out, carryIn, b[0]);
  xor xor_2 (xor_2_out, carryIn, b[1]);
  xor xor_3 (xor_3_out, carryIn, b[2]);
  soma soma_1 (.a(xor_1_out), .b(a[0]), .carryIn(carryIn), .soma(out_4[0]), .carryOut(soma_1_carryout));
  soma soma_2 (.a(xor_2_out), .b(a[1]), .carryIn(soma_1_carryout), .soma(out_4[1]), .carryOut(soma_2_carryout));
  soma soma_3 (.a(a[2]), .b(xor_3_out), .carryIn(soma_2_carryout), .soma(out_4[2]), .carryOut(soma_3_carryout));
  xor xor_4 (soma, soma_3_carryout, carryIn);

  // Notes on the sheet:
  //   carryIn
  //   0      soma
  //   1       diferença
endmodule

module compac (
  input  [2:0] a,
  input  [2:0] b,
  input  carryIn,
  output [2:0] sum_diff,
  output carryOut
);

  sum_diff sum_diff_1 (.a(a), .b(b), .carryIn(carryIn), .out_4(sum_diff), .soma(carryOut));

  // Notes on the sheet:
  //   carryIn
  //   0      soma
  //   1       diferença
endmodule
