// Logisim project Exemplo0021.circ as structural Verilog: 3 circuits, main circuit main
module main (
  input  carryIn,
  input  [2:0] a,
  input  [2:0] b,
  output [2:0] s,
  output carryOut
);

  FullAdder3b fulladder3b_1 (.a(a), .b(b), .carryIn(carryIn), .carryOut(carryOut), .s(s));
endmodule

// ADD
module FullAdder3b (
  input  carryIn,
  input  [2:0] a,
  input  [2:0] b,
  output [2:0] s,
  output carryOut
);

  wire fulladder_1_carryout, fulladder_2_carryout;

  FullAdder fulladder_1 (.a(a[0]), .b(b[0]), .CarryIn(carryIn), .carryOut(fulladder_1_carryout), .s(s[0]));
  FullAdder fulladder_2 (.a(a[1]), .b(b[1]), .CarryIn(fulladder_1_carryout), .carryOut(fulladder_2_carryout), .s(s[1]));
  FullAdder fulladder_3 (.a(a[2]), .b(b[2]), .CarryIn(fulladder_2_carryout), .carryOut(carryOut), .s(s[2]));
endmodule

// ADD
module FullAdder (
  input  CarryIn,
  input  a,
  input  b,
  output s,
  output carryOut
);

  wire and_1_out, and_2_out, and_3_out, xor_1_out;

  and and_1 (and_1_out, a, b);
  xor xor_1 (xor_1_out, a, b);
  and and_2 (and_2_out, a, CarryIn);
  and and_3 (and_3_out, b, CarryIn);
  or or_1 (carryOut, and_1_out, and_2_out, and_3_out);
  xor xor_2 (s, xor_1_out, CarryIn);
endmodule
