// Logisim project Exemplo0022.circ as structural Verilog: 3 circuits, main circuit main
module main (
  input  carryIn,
  input  [2:0] a,
  input  [2:0] b,
  output [2:0] s,
  output carryOut
);

  FullSub3b fullsub3b_1 (.a(a), .b(b), .carryIn(carryIn), .carryOut(carryOut), .s(s));
endmodule

// SUB
module FullSub3b (
  input  carryIn,
  input  [2:0] a,
  input  [2:0] b,
  output [2:0] s,
  output carryOut
);

  wire fullsub_1_carryout, fullsub_2_carryout;

  FullSub fullsub_1 (.a(a[0]), .b(b[0]), .CarryIn(carryIn), .carryOut(fullsub_1_carryout), .s(s[0]));
  FullSub fullsub_2 (.a(a[1]), .b(b[1]), .CarryIn(fullsub_1_carryout), .carryOut(fullsub_2_carryout), .s(s[1]));
  FullSub fullsub_3 (.a(a[2]), .b(b[2]), .CarryIn(fullsub_2_carryout), .carryOut(carryOut), .s(s[2]));
endmodule

// SUB
module FullSub (
  input  CarryIn,
  input  a,
  input  b,
  output s,
  output carryOut
);

  wire and_1_out, and_2_out, not_1_out, xor_1_out;

  xor xor_1 (xor_1_out, CarryIn, b);
  not not_1 (not_1_out, a);
  and and_1 (and_1_out, b, CarryIn);
  and and_2 (and_2_out, not_1_out, xor_1_out);
  or or_1 (carryOut, and_1_out, and_2_out);
  xor xor_2 (s, a, xor_1_out);
endmodule
