// Logisim project Exemplo0023.circ as structural Verilog: 2 circuits, main circuit main
module main (
  input  [2:0] a,
  input  [2:0] b,
  output s
);

  compI3b compi3b_1 (.a(a), .b(b), .s(s));
endmodule

// ==
module compI3b (
  input  [2:0] a,
  input  [2:0] b,
  output s
);

  wire xnor_1_out, xnor_2_out, xnor_3_out;

  xnor xnor_1 (xnor_1_out, a[0], b[0]);
  xnor xnor_2 (xnor_2_out, a[1], b[1]);
  xnor xnor_3 (xnor_3_out, a[2], b[2]);
  and and_1 (s, xnor_1_out, xnor_2_out, xnor_3_out);
endmodule
