// Logisim project Exemplo0024.circ as structural Verilog: 2 circuits, main circuit main
module main (
  input  [2:0] a,
  input  [2:0] b,
  output s
);

  compD3b compd3b_1 (.a(a), .b(b), .s(s));
endmodule

// !=
module compD3b (
  input  [2:0] a,
  input  [2:0] b,
  output s
);

  wire xor_1_out, xor_2_out, xor_3_out;

  xor xor_1 (xor_1_out, a[0], b[0]);
  xor xor_2 (xor_2_out, a[1], b[1]);
  xor xor_3 (xor_3_out, a[2], b[2]);
  or or_1 (s, xor_1_out, xor_2_out, xor_3_out);
endmodule
