// Logisim project Exemplo0025.circ as structural Verilog: 4 circuits, main circuit main
module main (
  input  [2:0] a,
  output [2:0] s
);

  comple23b comple23b_1 (.a(a), .s(s));
endmodule

// C2
module comple23b (
  input  [2:0] a,
  output [2:0] s
);

  wire [2:0] comple13b_1_s;

  comple13b comple13b_1 (.a(a), .s(comple13b_1_s));
  ADD1 add1_1 (.a(comple13b_1_s), .s(s));
endmodule

// C1
module comple13b (
  input  [2:0] a,
  output [2:0] s
);

  not not_1 (s[0], a[0]);
  not not_2 (s[1], a[1]);
  not not_3 (s[2], a[2]);
endmodule

// +1
module ADD1 (
  input  [2:0] a,
  output [2:0] s
);

  wire and_1_out;

  and and_1 (and_1_out, a[1], a[0]);
  not not_1 (s[0], a[0]);
  xor xor_1 (s[1], a[0], a[1]);
  xor xor_2 (s[2], and_1_out, a[2]);
endmodule
