// Logisim project Exemplo0026.circ as structural Verilog: 8 circuits, main circuit main
module main (
  input  carryIn,
  input  [2:0] a,
  input  [2:0] b,
  output [2:0] s,
  output carryOut
);

  addESub3b addesub3b_1 (.a(a), .b(b), .carryIn(carryIn), .carryOut(carryOut), .s(s));

  // Notes on the sheet:
  //   carryIn seleciona soma ou subtracao ( 0 ou 1 )
  //   carryOut nao tem valor nessa representação.
endmodule

// +|-
module addESub3b (
  input  carryIn,
  input  [2:0] a,
  input  [2:0] b,
  output [2:0] s,
  output carryOut
);

  wire fulladder_1_carryout, fulladder_2_carryout;
  wire [2:0] comple23b_1_s, mux2in3b_1_s;

  comple23b comple23b_1 (.a(b), .s(comple23b_1_s));
  mux2IN3b mux2in3b_1 (.a(b), .b(comple23b_1_s), .\seleção (carryIn), .s(mux2in3b_1_s));
  FullAdder fulladder_1 (.a(a[0]), .b(mux2in3b_1_s[0]), .CarryIn(1'b0), .carryOut(fulladder_1_carryout), .s(s[0]));
  FullAdder fulladder_2 (
    .a(a[1]), .b(mux2in3b_1_s[1]), .CarryIn(fulladder_1_carryout), .carryOut(fulladder_2_carryout), .s(s[1]));
  FullAdder fulladder_3 (.a(a[2]), .b(mux2in3b_1_s[2]), .CarryIn(fulladder_2_carryout), .carryOut(carryOut), .s(s[2]));
endmodule

// ADD
module FullAdder (
  input  CarryIn,
  input  a,
  input  b,
  output s,
  output carryOut
);

  wire and_1_out, and_2_out, and_3_out, xor_1_out;

  and and_1 (and_1_out, a, b);
  xor xor_1 (xor_1_out, a, b);
  and and_2 (and_2_out, a, CarryIn);
  and and_3 (and_3_out, b, CarryIn);
  or or_1 (carryOut, and_1_out, and_2_out, and_3_out);
  xor xor_2 (s, xor_1_out, CarryIn);
endmodule

// C2
module comple23b (
  input  [2:0] a,
  output [2:0] s
);

  wire [2:0] comple13b_1_s;

  comple13b comple13b_1 (.a(a), .s(comple13b_1_s));
  ADD1 add1_1 (.a(comple13b_1_s), .s(s));
endmodule

// C1
module comple13b (
  input  [2:0] a,
  output [2:0] s
);

  not not_1 (s[0], a[0]);
  not not_2 (s[1], a[1]);
  not not_3 (s[2], a[2]);
endmodule

// +1
module ADD1 (
  input  [2:0] a,
  output [2:0] s
);

  wire and_1_out;

  and and_1 (and_1_out, a[1], a[0]);
  not not_1 (s[0], a[0]);
  xor xor_1 (s[1], a[0], a[1]);
  xor xor_2 (s[2], and_1_out, a[2]);
endmodule

// M23
module mux2IN3b (
  input  [2:0] a,
  input  [2:0] b,
  input  \seleção ,
  output [2:0] s
);

  mux mux_1 (.a(a[0]), .b(b[0]), .\seleção (\seleção ), .s(s[0]));
  mux mux_2 (.a(a[1]), .b(b[1]), .\seleção (\seleção ), .s(s[1]));
  mux mux_3 (.a(a[2]), .b(b[2]), .\seleção (\seleção ), .s(s[2]));
endmodule

// MUX
module mux (
  input  a,
  input  b,
  input  \seleção ,
  output s
);

  wire and_1_out, and_2_out, not_1_out;

  not not_1 (not_1_out, \seleção );
  and and_1 (and_1_out, not_1_out, a);
  and and_2 (and_2_out, b, \seleção );
  or or_1 (s, and_1_out, and_2_out);
endmodule
