// Logisim project Exemplo0027.circ as structural Verilog: 3 circuits, main circuit main
module main (
  input  [2:0] a,
  input  [2:0] b,
  input  chave,
  output s
);

  compIeD3b compied3b_1 (.a(a), .b(b), .chave(chave), .s(s));

  // Notes on the sheet:
  //   chave = 1 | Desigualdade para saida em 1
  //   chave = 0 | Igualdade para saida em 1
endmodule

// CID
module compIeD3b (
  input  [2:0] a,
  input  [2:0] b,
  input  chave,
  output s
);

  wire not_1_out, or_1_out, xor_1_out, xor_2_out, xor_3_out;

  xor xor_1 (xor_1_out, a[0], b[0]);
  xor xor_2 (xor_2_out, a[1], b[1]);
  xor xor_3 (xor_3_out, a[2], b[2]);
  or or_1 (or_1_out, xor_1_out, xor_2_out, xor_3_out);
  mux mux_1 (.a(not_1_out), .b(or_1_out), .\seleção (chave), .s(s));
  not not_1 (not_1_out, or_1_out);
endmodule

// MUX
module mux (
  input  a,
  input  b,
  input  \seleção ,
  output s
);

  wire and_1_out, and_2_out, not_1_out;

  not not_1 (not_1_out, \seleção );
  and and_1 (and_1_out, not_1_out, a);
  and and_2 (and_2_out, b, \seleção );
  or or_1 (s, and_1_out, and_2_out);
endmodule
