// Logisim project Exemplo0021.circ as structural Verilog: 4 circuits, main circuit main
// H.A
module halfAdder (
  input  a,
  input  b,
  output s0,
  output s1
);

  xor xor_1 (s0, b, a);
  and and_1 (s1, b, a);
endmodule

// F.A.
module fullAdder (
  input  a,
  input  b,
  input  Carry_In,
  output s,
  output Carry_Out
);

  wire halfadder_1_s1, halfadder_2_s0, halfadder_2_s1;

  halfAdder halfadder_1 (.s0(s), .s1(halfadder_1_s1), .a(halfadder_2_s0), .b(Carry_In));
  halfAdder halfadder_2 (.s0(halfadder_2_s0), .s1(halfadder_2_s1), .a(a), .b(b));
  or or_1 (Carry_Out, halfadder_1_s1, halfadder_2_s1);

  // Notes on the sheet:
  //   w0
  //   w2
  //   w1
endmodule

module main (
  input  [2:0] a,
  input  [2:0] b,
  output CarryOut,
  output [3:0] out_4
);

  // Probe on a
  FullAdder3bits fulladder3bits_1 (.CarryOut(CarryOut), .in_1(a), .in_2(b), .soma(out_4[2:0]));
  // Probe on b
  // Probe on out_4[2:0]

  assign out_4[3] = CarryOut;
endmodule

// F.A
module FullAdder3bits (
  input  [2:0] in_1,
  input  [2:0] in_2,
  output CarryOut,
  output [2:0] soma
);

  wire fulladder_2_carry_out, fulladder_3_carry_out;

  fullAdder fulladder_1 (.s(soma[2]), .Carry_Out(CarryOut), .a(in_2[2]), .b(in_1[2]), .Carry_In(fulladder_2_carry_out));
  fullAdder fulladder_2 (
    .s(soma[1]), .Carry_Out(fulladder_2_carry_out), .a(in_1[1]), .b(in_2[1]), .Carry_In(fulladder_3_carry_out));
  fullAdder fulladder_3 (.s(soma[0]), .Carry_Out(fulladder_3_carry_out), .a(in_1[0]), .b(in_2[0]), .Carry_In(1'b0));
endmodule
