// Logisim project Exemplo0022.circ as structural Verilog: 3 circuits, main circuit main
// H.A.
module HalfAdder (
  input  a,
  input  b,
  output s1,
  output s0
);

  and and_1 (s1, a, b);
  xor xor_1 (s0, a, b);
endmodule

// F.A.
module FullAdder (
  input  a,
  input  b,
  input  carry_In,
  output carry_Out,
  output s
);

  wire halfadder_1_s0, halfadder_1_s1, halfadder_2_s1;

  or or_1 (carry_Out, halfadder_1_s1, halfadder_2_s1);
  HalfAdder halfadder_1 (.a(a), .b(b), .s1(halfadder_1_s1), .s0(halfadder_1_s0));
  HalfAdder halfadder_2 (.a(halfadder_1_s0), .b(carry_In), .s1(halfadder_2_s1), .s0(s));
endmodule

module main (
  input  [2:0] a,
  input  [2:0] b,
  output [2:0] s
);

  wire fulladder_2_carry_out, fulladder_3_carry_out, not_1_out, not_2_out, not_3_out;

  // Probe on a
  not not_1 (not_1_out, b[2]);
  FullAdder fulladder_1 (.a(a[2]), .b(not_1_out), .s(s[2]), .carry_In(fulladder_2_carry_out));  // open: carry_Out
  // Probe on s
  // Probe on b
  not not_2 (not_2_out, b[1]);
  FullAdder fulladder_2 (
    .carry_Out(fulladder_2_carry_out), .a(a[1]), .b(not_2_out), .s(s[1]), .carry_In(fulladder_3_carry_out));
  not not_3 (not_3_out, b[0]);
  FullAdder fulladder_3 (.carry_Out(fulladder_3_carry_out), .a(a[0]), .b(not_3_out), .s(s[0]), .carry_In(1'b1));
endmodule
