// Logisim project Exemplo0024.circ as structural Verilog: 1 circuit, main circuit main
module main (
  input  [2:0] a,
  input  [2:0] b,
  output out_3
);

  wire [2:0] xnor_1_out;

  assign xnor_1_out = ~(a ^ b);  // XNOR_Gate xnor_1, 3 bits wide
  nand nand_1 (out_3, xnor_1_out[2], xnor_1_out[1], xnor_1_out[0]);
endmodule
