// Logisim project circuitos.circ as structural Verilog: 8 circuits, main circuit HALF-ADDER
// H.A
module HALF_ADDER (
  input  A,
  input  B,
  output S0,
  output S1
);

  xor xor_1 (S0, B, A);
  and and_1 (S1, B, A);
endmodule

// F/A
module FULL_ADDER (
  input  A,
  input  B,
  input  CARRY_IN,
  output S0,
  output S1
);

  wire half_adder_1_s0, half_adder_1_s1, half_adder_2_s1;

  HALF_ADDER half_adder_1 (.A(A), .B(B), .S0(half_adder_1_s0), .S1(half_adder_1_s1));
  HALF_ADDER half_adder_2 (.A(half_adder_1_s0), .B(CARRY_IN), .S0(S0), .S1(half_adder_2_s1));
  or or_1 (S1, half_adder_1_s1, half_adder_2_s1);
endmodule

module Exemplo_0031 (
  input  [2:0] A,
  input  [2:0] B,
  input  CARRY_IN,
  output overFlow,
  output [2:0] out_5
);

  wire full_adder_1_s1, full_adder_2_s1, xor_1_out, xor_2_out, xor_3_out;

  // Probe on A
  // Probe on B
  xor xor_1 (xor_1_out, CARRY_IN, B[0]);
  FULL_ADDER full_adder_1 (.A(A[0]), .B(xor_1_out), .CARRY_IN(CARRY_IN), .S0(out_5[2]), .S1(full_adder_1_s1));
  xor xor_2 (xor_2_out, CARRY_IN, B[1]);
  FULL_ADDER full_adder_2 (.A(A[1]), .B(xor_2_out), .CARRY_IN(full_adder_1_s1), .S0(out_5[1]), .S1(full_adder_2_s1));
  xor xor_3 (xor_3_out, CARRY_IN, B[2]);
  FULL_ADDER full_adder_3 (.A(A[2]), .B(xor_3_out), .CARRY_IN(full_adder_2_s1), .S0(out_5[0]), .S1(overFlow));
  // Probe on out_5

  // Notes on the sheet:
  //   0-ADDER
  //   1-SUBTRACTOR
  //   Exemplo_0031
  //   Milton costa teles da silva - 002751
endmodule

module Exemplo_0032 (
  input  [2:0] A,
  input  [2:0] B,
  input  CARRY_IN,
  output overFlow,
  output [2:0] out_5,
  output Resultado_da
);

  wire full_adder_1_s1, full_adder_2_s1, xor_1_out, xor_2_out, xor_3_out;

  // Probe on A
  // Probe on B
  xor xor_1 (xor_1_out, CARRY_IN, B[0]);
  FULL_ADDER full_adder_1 (.A(A[0]), .B(xor_1_out), .CARRY_IN(CARRY_IN), .S0(out_5[2]), .S1(full_adder_1_s1));
  xor xor_2 (xor_2_out, CARRY_IN, B[1]);
  FULL_ADDER full_adder_2 (.A(A[1]), .B(xor_2_out), .CARRY_IN(full_adder_1_s1), .S0(out_5[1]), .S1(full_adder_2_s1));
  xor xor_3 (xor_3_out, CARRY_IN, B[2]);
  FULL_ADDER full_adder_3 (.A(A[2]), .B(xor_3_out), .CARRY_IN(full_adder_2_s1), .S0(out_5[0]), .S1(overFlow));
  // Probe on out_5
  nor nor_1 (Resultado_da, out_5[0], out_5[1], out_5[2]);

  // Notes on the sheet:
  //   0-ADDER
  //   1-SUBTRACTOR
  //   Exemplo_0032
  //   Milton costa teles da silva - 002751
  //   operacao = 0
  //   1 - sim
  //   0 - nao
endmodule

module Exemplo_0033 (
  input  [2:0] A,
  output OVERFLOW,
  output [2:0] s1
);

  wire full_adder_1_s1, full_adder_2_s1;

  // Probe on A
  FULL_ADDER full_adder_1 (.A(A[0]), .B(1'b0), .CARRY_IN(1'b1), .S0(s1[0]), .S1(full_adder_1_s1));
  FULL_ADDER full_adder_2 (.A(A[1]), .B(1'b0), .CARRY_IN(full_adder_1_s1), .S0(s1[1]), .S1(full_adder_2_s1));
  FULL_ADDER full_adder_3 (.A(A[2]), .B(1'b0), .CARRY_IN(full_adder_2_s1), .S0(s1[2]), .S1(OVERFLOW));
  // Probe on s1

  // Notes on the sheet:
  //   Exemplo_0033
  //   Milton costa teles da silva - 002751
endmodule

module Extra_01 (
  input  [2:0] A,
  output OVERFLOW,
  output [2:0] s1
);

  wire full_adder_1_s1, full_adder_2_s1;

  // Probe on A
  FULL_ADDER full_adder_1 (.A(A[0]), .B(1'b1), .CARRY_IN(1'b0), .S0(s1[0]), .S1(full_adder_1_s1));
  FULL_ADDER full_adder_2 (.A(A[1]), .B(1'b1), .CARRY_IN(full_adder_1_s1), .S0(s1[1]), .S1(full_adder_2_s1));
  FULL_ADDER full_adder_3 (.A(A[2]), .B(1'b1), .CARRY_IN(full_adder_2_s1), .S0(s1[2]), .S1(OVERFLOW));
  // Probe on s1

  // Notes on the sheet:
  //   Extra_01
  //   Milton costa teles da silva - 002751
endmodule

module Exemplo_0034 (
  input  [2:0] A,
  input  [2:0] B,
  input  CARRY_IN,
  output [2:0] out_4,
  output detector_de_overFlow,
  output out_6
);

  wire full_adder_1_s1, full_adder_2_s1, full_adder_3_s1, xor_1_out, xor_2_out, xor_3_out, xor_4_out,
       xor_5_out;

  // Probe on A
  // Probe on B
  xor xor_1 (xor_1_out, CARRY_IN, CARRY_IN);
  xor xor_2 (xor_2_out, CARRY_IN, B[0]);
  FULL_ADDER full_adder_1 (.A(A[0]), .B(xor_2_out), .CARRY_IN(CARRY_IN), .S0(out_4[2]), .S1(full_adder_1_s1));
  xor xor_3 (xor_3_out, CARRY_IN, B[1]);
  FULL_ADDER full_adder_2 (.A(A[1]), .B(xor_3_out), .CARRY_IN(full_adder_1_s1), .S0(out_4[1]), .S1(full_adder_2_s1));
  xor xor_4 (xor_4_out, CARRY_IN, B[2]);
  FULL_ADDER full_adder_3 (.A(A[2]), .B(xor_4_out), .CARRY_IN(full_adder_2_s1), .S0(out_4[0]), .S1(full_adder_3_s1));
  xor xor_5 (xor_5_out, full_adder_3_s1, full_adder_3_s1);
  or or_1 (detector_de_overFlow, full_adder_3_s1, xor_1_out);
  or or_2 (out_6, xor_5_out, CARRY_IN);
  // Probe on out_4

  // Notes on the sheet:
  //   0-ADDER
  //   1-SUBTRACTOR
  //   Exemplo_0034
  //   Milton costa teles da silva - 002751
  //   detector de carryn
endmodule

module Exemplo_35 (
  input  [2:0] A,
  input  [2:0] B,
  input  CARRY_IN,
  output overFlow,
  output [2:0] out_5,
  output out_6
);

  wire full_adder_1_s1, full_adder_2_s1, xor_1_out, xor_2_out, xor_3_out, xor_4_out;

  // Probe on A
  // Probe on B
  xor xor_1 (xor_1_out, CARRY_IN, B[0]);
  FULL_ADDER full_adder_1 (.A(A[0]), .B(xor_1_out), .CARRY_IN(CARRY_IN), .S0(out_5[2]), .S1(full_adder_1_s1));
  xor xor_2 (xor_2_out, CARRY_IN, B[1]);
  FULL_ADDER full_adder_2 (.A(A[1]), .B(xor_2_out), .CARRY_IN(full_adder_1_s1), .S0(out_5[1]), .S1(full_adder_2_s1));
  xor xor_3 (xor_3_out, CARRY_IN, B[2]);
  FULL_ADDER full_adder_3 (.A(A[2]), .B(xor_3_out), .CARRY_IN(full_adder_2_s1), .S0(out_5[0]), .S1(overFlow));
  xor xor_4 (xor_4_out, overFlow, overFlow);
  // Probe on out_5
  or or_1 (out_6, xor_4_out, CARRY_IN);

  // Notes on the sheet:
  //   Exemplo_0035
  //   Milton costa teles da silva - 002751
  //   detector de sinal
  //   0-plus
  //   1-minus
endmodule
