// Logisim project Exemplo0037.circ as structural Verilog: 2 circuits, main circuit main
module main (
  input  in_1,
  input  in_2,
  input  in_3,
  input  in_4,
  input  in_5,
  input  in_6,
  output out_7,
  output out_8,
  output out_9
);

  wire comparador_1_s0, comparador_1_s1, comparador_2_s0, comparador_2_s1;

  Comparador comparador_1 (.c0(1'b0), .c1(1'b1), .a(in_1), .b(in_2), .s0(comparador_1_s0), .s1(comparador_1_s1));
  Comparador comparador_2 (
    .c0(comparador_1_s0), .c1(comparador_1_s1), .a(in_3), .b(in_4), .s0(comparador_2_s0), .s1(comparador_2_s1));
  Comparador comparador_3 (.c0(comparador_2_s0), .c1(comparador_2_s1), .a(in_5), .b(in_6), .s0(out_7), .s1(out_8));
  xnor xnor_1 (out_9, out_8, out_7);
endmodule

// CA
module Comparador (
  input  a,
  input  b,
  input  c0,
  input  c1,
  output s0,
  output s1
);

  wire and_1_out, and_2_out, and_3_out, and_4_out, not_1_out, not_2_out;

  not not_1 (not_1_out, b);
  not not_2 (not_2_out, a);
  or or_1 (s0, c0, and_1_out);
  and and_1 (and_1_out, not_1_out, a, c1);
  and and_2 (and_2_out, not_1_out, not_2_out, c1);
  and and_3 (and_3_out, b, a, c1);
  or or_2 (s1, and_2_out, and_3_out, and_4_out);
  and and_4 (and_4_out, c0, c1);
endmodule
