// Logisim project Exemplo0031.circ as structural Verilog: 3 circuits, main circuit main
module main (
  input  [5:0] in_1,
  input  [5:0] in_2,
  input  in_3,
  output out_4,
  output out_5,
  output out_6,
  output out_7,
  output out_8,
  output out_9,
  output Overf
);

  wire selecionar_1_s1, selecionar_2_s1, selecionar_3_s1, selecionar_4_s1, selecionar_6_s1;

  Selecionar selecionar_1 (
    .x(in_1[0]), .y(in_2[0]), .C_in(in_3), .Selecionador(in_3), .s0(out_4), .s1(selecionar_1_s1));
  Selecionar selecionar_2 (
    .x(in_1[1]), .y(in_2[1]), .C_in(selecionar_1_s1), .Selecionador(in_3), .s0(out_5), .s1(selecionar_2_s1));
  Selecionar selecionar_3 (
    .x(in_1[2]), .y(in_2[2]), .C_in(selecionar_2_s1), .Selecionador(in_3), .s0(out_6), .s1(selecionar_3_s1));
  Selecionar selecionar_4 (
    .x(in_1[3]), .y(in_2[3]), .C_in(selecionar_3_s1), .Selecionador(in_3), .s0(out_7), .s1(selecionar_4_s1));
  Selecionar selecionar_5 (
    .x(in_1[4]), .y(in_2[4]), .C_in(selecionar_4_s1), .Selecionador(in_3), .s0(out_8));  // open: s1
  Selecionar selecionar_6 (
    .x(in_1[5]), .y(in_2[5]), .C_in(in_3), .Selecionador(in_3), .s0(out_9), .s1(selecionar_6_s1));
  xor xor_1 (Overf, in_3, selecionar_6_s1);

  // Notes on the sheet:
  //   soma = carryIn = 0
  //   subtraçao = carryIn  = 1
  //   Exemplo0031 - João Henrique Mendes de Oliveira - 392734
endmodule

module full_adder (
  input  C_in,
  input  x,
  input  y,
  output s0,
  output s1
);

  wire and_1_out, and_2_out, xor_1_out;

  xor xor_1 (xor_1_out, x, y);
  and and_1 (and_1_out, x, y);
  xor xor_2 (s0, C_in, xor_1_out);
  and and_2 (and_2_out, C_in, xor_1_out);
  or or_1 (s1, and_2_out, and_1_out);
endmodule

module Selecionar (
  input  x,
  input  y,
  input  C_in,
  input  Selecionador,
  output s0,
  output s1
);

  wire xor_1_out;

  xor xor_1 (xor_1_out, y, Selecionador);
  full_adder full_adder_1 (.C_in(C_in), .x(x), .y(xor_1_out), .s0(s0), .s1(s1));
endmodule
