// Logisim project Exemplos.circ as structural Verilog: 10 circuits, main circuit FullAdder
// FAx4
module Exemplo0031 (
  input  [2:0] a,
  input  [2:0] b,
  input  Carry_in,
  output Carry_out,
  output [2:0] Saida
);

  wire fulladder_1_carry_out, fulladder_2_carry_out, fulladder_3_carry_out;
  wire [2:0] xor_2_out;

  xor xor_1 (Carry_out, Carry_in, fulladder_1_carry_out);
  FullAdder fulladder_1 (
    .carry_in(fulladder_2_carry_out), .carry_out(fulladder_1_carry_out), .a(a[2]), .b(xor_2_out[2]),
    .s(Saida[2]));
  FullAdder fulladder_2 (
    .carry_in(fulladder_3_carry_out), .carry_out(fulladder_2_carry_out), .a(a[1]), .b(xor_2_out[1]),
    .s(Saida[1]));
  assign xor_2_out = b ^ {3{Carry_in}};  // XOR_Gate xor_2, 3 bits wide
  FullAdder fulladder_3 (
    .carry_in(Carry_in), .carry_out(fulladder_3_carry_out), .a(a[0]), .b(xor_2_out[0]), .s(Saida[0]));

  // Notes on the sheet:
  //   exercicio 01
endmodule

module Exemplo0032 (
  input  [2:0] a,
  input  [2:0] b,
  input  Carry_in,
  output Carry_out,
  output Equals_0,
  output [2:0] Saida
);

  wire equals_0_1_out_2, equals_0_2_out_2, equals_0_3_out_2, fulladder_1_carry_out, fulladder_2_carry_out,
       fulladder_3_carry_out;
  wire [2:0] xor_2_out;

  xor xor_1 (Carry_out, Carry_in, fulladder_2_carry_out);
  FullAdder fulladder_1 (
    .carry_in(fulladder_3_carry_out), .carry_out(fulladder_1_carry_out), .a(a[1]), .b(xor_2_out[1]),
    .s(Saida[1]));
  FullAdder fulladder_2 (
    .carry_in(fulladder_1_carry_out), .carry_out(fulladder_2_carry_out), .a(a[2]), .b(xor_2_out[2]),
    .s(Saida[2]));
  FullAdder fulladder_3 (
    .carry_in(Carry_in), .carry_out(fulladder_3_carry_out), .a(a[0]), .b(xor_2_out[0]), .s(Saida[0]));
  Equals_0 equals_0_1 (.in_1(Saida[0]), .out_2(equals_0_1_out_2));
  Equals_0 equals_0_2 (.in_1(Saida[1]), .out_2(equals_0_2_out_2));
  Equals_0 equals_0_3 (.in_1(Saida[2]), .out_2(equals_0_3_out_2));
  assign xor_2_out = b ^ {3{Carry_in}};  // XOR_Gate xor_2, 3 bits wide
  and and_1 (Equals_0, equals_0_1_out_2, equals_0_2_out_2, equals_0_3_out_2);

  // Notes on the sheet:
  //   exercicio 02
endmodule

module Exemplo0033 (
  input  [2:0] a,
  input  [2:0] b,
  input  Carry_in,
  output Carry_out,
  output Equals_0,
  output [2:0] Saida
);

  wire equals_0_1_out_2, equals_0_2_out_2, equals_0_3_out_2, fulladder_1_carry_out, fulladder_2_carry_out,
       fulladder_3_carry_out;
  wire [2:0] plus_minus_1_1_out_3, xor_2_out;

  xor xor_1 (Carry_out, Carry_in, fulladder_1_carry_out);
  Plus_Minus_1 plus_minus_1_1 (._0____1____1____1(1'b0), .a(a), .out_3(plus_minus_1_1_out_3));
  FullAdder fulladder_1 (
    .carry_in(fulladder_2_carry_out), .carry_out(fulladder_1_carry_out), .a(plus_minus_1_1_out_3[2]),
    .b(xor_2_out[2]), .s(Saida[2]));
  FullAdder fulladder_2 (
    .carry_in(fulladder_3_carry_out), .carry_out(fulladder_2_carry_out), .a(plus_minus_1_1_out_3[1]),
    .b(xor_2_out[1]), .s(Saida[1]));
  FullAdder fulladder_3 (
    .carry_in(Carry_in), .carry_out(fulladder_3_carry_out), .a(plus_minus_1_1_out_3[0]), .b(xor_2_out[0]),
    .s(Saida[0]));
  Equals_0 equals_0_1 (.in_1(Saida[0]), .out_2(equals_0_1_out_2));
  Equals_0 equals_0_2 (.in_1(Saida[1]), .out_2(equals_0_2_out_2));
  Equals_0 equals_0_3 (.in_1(Saida[2]), .out_2(equals_0_3_out_2));
  assign xor_2_out = b ^ {3{Carry_in}};  // XOR_Gate xor_2, 3 bits wide
  and and_1 (Equals_0, equals_0_1_out_2, equals_0_2_out_2, equals_0_3_out_2);

  // Notes on the sheet:
  //   exercicio 03
endmodule

module Exemplo0034 (
  input  [2:0] a,
  input  [2:0] b,
  input  Carry_in,
  output Carry_out,
  output Teste,
  output [2:0] Saida
);

  wire equals_0_1_out_2, equals_0_2_out_2, equals_0_3_out_2, fulladder_1_carry_out, fulladder_2_carry_out,
       fulladder_3_carry_out;
  wire [2:0] plus_minus_1_1_out_3, xor_2_out;

  xor xor_1 (Carry_out, Carry_in, fulladder_1_carry_out);
  Plus_Minus_1 plus_minus_1_1 (._0____1____1____1(1'b1), .a(a), .out_3(plus_minus_1_1_out_3));
  FullAdder fulladder_1 (
    .carry_in(fulladder_2_carry_out), .carry_out(fulladder_1_carry_out), .a(plus_minus_1_1_out_3[2]),
    .b(xor_2_out[2]), .s(Saida[2]));
  FullAdder fulladder_2 (
    .carry_in(fulladder_3_carry_out), .carry_out(fulladder_2_carry_out), .a(plus_minus_1_1_out_3[1]),
    .b(xor_2_out[1]), .s(Saida[1]));
  assign xor_2_out = b ^ {3{Carry_in}};  // XOR_Gate xor_2, 3 bits wide
  FullAdder fulladder_3 (
    .carry_in(Carry_in), .carry_out(fulladder_3_carry_out), .a(plus_minus_1_1_out_3[0]), .b(xor_2_out[0]),
    .s(Saida[0]));
  Equals_0 equals_0_1 (.in_1(Saida[0]), .out_2(equals_0_1_out_2));
  Equals_0 equals_0_2 (.in_1(Saida[1]), .out_2(equals_0_2_out_2));
  Equals_0 equals_0_3 (.in_1(Saida[2]), .out_2(equals_0_3_out_2));
  and and_1 (Teste, equals_0_1_out_2, equals_0_2_out_2, equals_0_3_out_2);

  // Notes on the sheet:
  //   exercicio 06
endmodule

module Exemplo0035 (
  input  [2:0] a,
  input  [2:0] b,
  output A___B,
  output A___B_2
);

  wire [1:0] exemplo0031_1_saida;

  Exemplo0031 exemplo0031_1 (.Carry_in(1'b1), .a(a), .b(b), .Saida({A___B, exemplo0031_1_saida}));  // open: Carry_out
  not not_1 (A___B_2, A___B);

  // Notes on the sheet:
  //   exercicio 07
endmodule

module Exemplo0036 (
  input  [2:0] a,
  input  [2:0] b,
  input  _0____1____1____1,
  input  Carry_in,
  output Overflow,
  output Teste,
  output [2:0] Saida
);

  wire equals_0_1_out_2, equals_0_2_out_2, equals_0_3_out_2, fulladder_1_carry_out, fulladder_2_carry_out,
       fulladder_3_carry_out;
  wire [2:0] plus_minus_1_1_out_3, xor_2_out;

  xor xor_1 (Overflow, Carry_in, fulladder_1_carry_out);
  Plus_Minus_1 plus_minus_1_1 (._0____1____1____1(_0____1____1____1), .a(a), .out_3(plus_minus_1_1_out_3));
  FullAdder fulladder_1 (
    .carry_in(fulladder_2_carry_out), .carry_out(fulladder_1_carry_out), .a(plus_minus_1_1_out_3[2]),
    .b(xor_2_out[2]), .s(Saida[2]));
  FullAdder fulladder_2 (
    .carry_in(fulladder_3_carry_out), .carry_out(fulladder_2_carry_out), .a(plus_minus_1_1_out_3[1]),
    .b(xor_2_out[1]), .s(Saida[1]));
  FullAdder fulladder_3 (
    .carry_in(Carry_in), .carry_out(fulladder_3_carry_out), .a(plus_minus_1_1_out_3[0]), .b(xor_2_out[0]),
    .s(Saida[0]));
  Equals_0 equals_0_1 (.in_1(Saida[0]), .out_2(equals_0_1_out_2));
  Equals_0 equals_0_2 (.in_1(Saida[1]), .out_2(equals_0_2_out_2));
  Equals_0 equals_0_3 (.in_1(Saida[2]), .out_2(equals_0_3_out_2));
  assign xor_2_out = b ^ {3{Carry_in}};  // XOR_Gate xor_2, 3 bits wide
  and and_1 (Teste, equals_0_1_out_2, equals_0_2_out_2, equals_0_3_out_2);

  // Notes on the sheet:
  //   exercicio 04
endmodule

module Exemplo0037 (
  input  [2:0] a,
  input  [2:0] b,
  input  _0____1____1____1,
  input  Carry_in,
  output Carry_out,
  output Teste,
  output [2:0] Saida
);

  wire equals_0_1_out_2, equals_0_2_out_2, equals_0_3_out_2, fulladder_1_carry_out, fulladder_2_carry_out,
       fulladder_3_carry_out;
  wire [2:0] plus_minus_1_1_out_3, xor_2_out;

  xor xor_1 (Carry_out, Carry_in, fulladder_1_carry_out);
  Plus_Minus_1 plus_minus_1_1 (._0____1____1____1(_0____1____1____1), .a(a), .out_3(plus_minus_1_1_out_3));
  FullAdder fulladder_1 (
    .carry_in(fulladder_3_carry_out), .carry_out(fulladder_1_carry_out), .a(plus_minus_1_1_out_3[2]),
    .b(xor_2_out[2]), .s(Saida[2]));
  FullAdder fulladder_2 (
    .carry_in(Carry_in), .carry_out(fulladder_2_carry_out), .a(plus_minus_1_1_out_3[0]), .b(xor_2_out[0]),
    .s(Saida[0]));
  FullAdder fulladder_3 (
    .carry_in(fulladder_2_carry_out), .carry_out(fulladder_3_carry_out), .a(plus_minus_1_1_out_3[1]),
    .b(xor_2_out[1]), .s(Saida[1]));
  Equals_0 equals_0_1 (.in_1(Saida[0]), .out_2(equals_0_1_out_2));
  Equals_0 equals_0_2 (.in_1(Saida[1]), .out_2(equals_0_2_out_2));
  Equals_0 equals_0_3 (.in_1(Saida[2]), .out_2(equals_0_3_out_2));
  assign xor_2_out = b ^ {3{Carry_in}};  // XOR_Gate xor_2, 3 bits wide
  and and_1 (Teste, equals_0_1_out_2, equals_0_2_out_2, equals_0_3_out_2);

  // Notes on the sheet:
  //   exercicio 05
endmodule

// T.I
module Equals_0 (
  input  in_1,
  output out_2
);

  nor nor_1 (out_2, in_1, 1'b0);
endmodule

// +/- 1
module Plus_Minus_1 (
  input  [2:0] a,
  input  _0____1____1____1,
  output [2:0] out_3
);

  wire exemplo0031_1_carry_out;

  Exemplo0031 exemplo0031_1 (
    .Carry_out(exemplo0031_1_carry_out), .Carry_in(_0____1____1____1), .a(a), .b(3'b001), .Saida(out_3));
endmodule

// F.A
module FullAdder (
  input  a,
  input  b,
  input  carry_in,
  output carry_out,
  output s
);

  wire and_1_out, and_2_out, xor_1_out;

  xor xor_1 (xor_1_out, b, a);
  and and_1 (and_1_out, a, b);
  and and_2 (and_2_out, xor_1_out, carry_in);
  or or_1 (carry_out, and_2_out, and_1_out);
  xor xor_2 (s, carry_in, xor_1_out);
endmodule
