// Logisim project Exemplo0031_Exemplo0032.circ as structural Verilog: 2 circuits, main circuit Exercicio0031
module Exercicio0031 (
  input  Carry_in,
  input  in_2,
  input  in_3,
  output out_4,
  output Carry_Out
);

  wire and_1_out, and_2_out, xor_1_out, xor_2_out;

  xor xor_1 (xor_1_out, in_3, in_2);
  and and_1 (and_1_out, in_3, in_2);
  xor xor_2 (xor_2_out, in_3, in_2);
  and and_2 (and_2_out, Carry_in, xor_1_out);
  xor xor_3 (out_4, xor_2_out, Carry_in);
  or or_1 (Carry_Out, and_2_out, and_1_out);
endmodule

module Exercicio0032 (
  input  Carry_in,
  input  in_2,
  input  in_3,
  output out_4,
  output out_5
);

  wire and_1_out, and_2_out, not_1_out, not_2_out, or_1_out;

  xor xor_1 (out_4, in_2, in_2);
  not not_1 (not_1_out, in_2);
  Exercicio0031 exercicio0031_1 (.Carry_in(in_2), .in_2(in_2), .in_3(in_2), .out_4(Carry_in), .Carry_Out(in_2));
  or or_1 (or_1_out, not_1_out, in_2);
  and and_1 (and_1_out, or_1_out, Carry_in);
  not not_2 (not_2_out, in_2);
  and and_2 (and_2_out, not_2_out, in_2);
  or or_2 (out_5, and_1_out, and_2_out);

  assign in_3 = in_2;

  // Notes on the sheet:
  //   Carry OUT
endmodule
