// Logisim project Exemplo0033.circ as structural Verilog: 4 circuits, main circuit Plus - Minus 1
// FAx4
module Exemplo0031 (
  input  [3:0] a,
  input  [3:0] b,
  input  Carry_in,
  output Carry_out,
  output [3:0] s
);

  wire full_adder_1_out_4, full_adder_2_out_4, full_adder_3_out_4, full_adder_4_out_4;
  wire [3:0] xor_2_out;

  xor xor_1 (Carry_out, Carry_in, full_adder_1_out_4);
  Full_Adder full_adder_1 (.in_3(full_adder_2_out_4), .out_4(full_adder_1_out_4), .a(a[3]), .b(xor_2_out[3]), .s(s[3]));
  Full_Adder full_adder_2 (.in_3(full_adder_3_out_4), .out_4(full_adder_2_out_4), .a(a[2]), .b(xor_2_out[2]), .s(s[2]));
  Full_Adder full_adder_3 (.in_3(full_adder_4_out_4), .out_4(full_adder_3_out_4), .a(a[1]), .b(xor_2_out[1]), .s(s[1]));
  assign xor_2_out = b ^ {4{Carry_in}};  // XOR_Gate xor_2, 4 bits wide
  Full_Adder full_adder_4 (.in_3(Carry_in), .out_4(full_adder_4_out_4), .a(a[0]), .b(xor_2_out[0]), .s(s[0]));
endmodule

// T.I
module Equals_0 (
  input  in_1,
  output s
);

  nor nor_1 (s, in_1, 1'b0);
endmodule

// +/- 1
module Plus___Minus_1 (
  input  [3:0] in_1,
  input  _0____1____1____1,
  output [3:0] out_3
);

  Exemplo0031 exemplo0031_1 (.Carry_in(_0____1____1____1), .a(in_1), .b(4'b0001), .s(out_3));  // open: Carry_out
endmodule

// F.A
module Full_Adder (
  input  a,
  input  b,
  input  in_3,
  output out_4,
  output s
);

  wire and_1_out, and_2_out, xor_1_out;

  xor xor_1 (xor_1_out, b, a);
  and and_1 (and_1_out, a, b);
  and and_2 (and_2_out, xor_1_out, in_3);
  xor xor_2 (s, in_3, xor_1_out);
  or or_1 (out_4, and_2_out, and_1_out);
endmodule
