// Logisim project Exemplo0034.circ as structural Verilog: 1 circuit, main circuit Exemplo0034
module Exemplo0034 (
  input  [3:0] in_1,
  output [3:0] out_2,
  output overFlow
);

  wire and_1_out, and_3_out, nor_1_out, not_1_out, or_1_out, xor_1_out;

  nor nor_1 (nor_1_out, in_1[0], in_1[1]);
  not not_1 (not_1_out, in_1[2]);
  xor xor_1 (xor_1_out, in_1[0], in_1[2]);
  and and_1 (and_1_out, ~in_1[1], in_1[2]);  // AND_Gate
  xor xor_2 (out_2[1], in_1[0], in_1[1]);
  not not_2 (out_2[0], in_1[0]);
  and and_2 (overFlow, in_1[0], in_1[1], in_1[2]);
  or or_1 (or_1_out, nor_1_out, not_1_out);
  and and_3 (and_3_out, xor_1_out, in_1[1]);
  and and_4 (out_2[3], in_1[3], or_1_out);
  or or_2 (out_2[2], and_3_out, and_1_out);
endmodule
