// Logisim project Exercicios.circ as structural Verilog: 9 circuits, main circuit FullAdder
// FA
module FullAdder (
  input  a,
  input  b,
  input  c,
  output s1,
  output s0
);

  wire and_1_out, and_2_out, xor_1_out;

  xor xor_1 (xor_1_out, b, a);
  and and_1 (and_1_out, b, a);
  xor xor_2 (s1, c, xor_1_out);
  and and_2 (and_2_out, xor_1_out, c);
  or or_1 (s0, and_2_out, and_1_out);
endmodule

// HA
module HalfAdder (
  input  a,
  input  b,
  output s1,
  output s0
);

  xor xor_1 (s1, b, a);
  and and_1 (s0, b, a);
endmodule

// HS
module HalfSub (
  input  a,
  input  b,
  output s1,
  output s0
);

  xor xor_1 (s1, b, a);
  and and_1 (s0, b, ~a);  // AND_Gate
endmodule

// FS
module FullSub (
  input  c,
  input  a,
  input  b,
  output s1,
  output s0
);

  wire and_1_out, and_2_out, xor_1_out;

  xor xor_1 (xor_1_out, b, a);
  and and_1 (and_1_out, b, ~a);  // AND_Gate
  xor xor_2 (s1, c, xor_1_out);
  and and_2 (and_2_out, c, ~xor_1_out);  // AND_Gate
  or or_1 (s0, and_2_out, and_1_out);
endmodule

// 0Flag
module ZeroFlag (
  input  in_1,
  input  [2:0] in_2,
  output out_3
);

  nor nor_1 (out_3, in_1, in_2[0], in_2[1], in_2[2]);
endmodule

// SA
module Exercicio01 (
  input  [2:0] x,
  input  [2:0] y,
  input  op,
  output carryOut,
  output [2:0] s
);

  wire fulladder_1_s0, fulladder_2_s0, fulladder_3_s0, xor_2_out, xor_3_out, xor_4_out;

  FullAdder fulladder_1 (.s1(s[2]), .s0(fulladder_1_s0), .a(xor_2_out), .b(x[2]), .c(fulladder_2_s0));
  xor xor_1 (carryOut, op, fulladder_1_s0);
  xor xor_2 (xor_2_out, op, y[2]);
  xor xor_3 (xor_3_out, op, y[1]);
  FullAdder fulladder_2 (.s1(s[1]), .s0(fulladder_2_s0), .a(xor_3_out), .b(x[1]), .c(fulladder_3_s0));
  xor xor_4 (xor_4_out, y[0], op);
  FullAdder fulladder_3 (.s1(s[0]), .s0(fulladder_3_s0), .a(xor_4_out), .b(x[0]), .c(op));
endmodule

module Exercicio02 (
  input  [2:0] x,
  input  [2:0] y,
  input  op,
  output out_4,
  output carryOut,
  output [2:0] s
);

  Exercicio01 exercicio01_1 (.x(x), .y(y), .op(op), .carryOut(carryOut), .s(s));
  ZeroFlag zeroflag_1 (.in_1(carryOut), .in_2(s), .out_3(out_4));
endmodule

module Inc1 (
  input  [2:0] x,
  output [3:0] y
);

  wire and_2_out, and_3_out, and_4_out, not_1_out, not_2_out, not_3_out;

  not not_1 (not_1_out, x[2]);
  not not_2 (not_2_out, x[1]);
  not not_3 (not_3_out, x[0]);
  not not_4 (y[0], x[0]);
  and and_1 (y[3], x[2], x[1], x[0]);
  and and_2 (and_2_out, not_1_out, x[1], x[0]);
  and and_3 (and_3_out, x[2], not_2_out);
  and and_4 (and_4_out, x[2], not_3_out);
  or or_1 (y[2], and_2_out, and_3_out, and_4_out);
  xor xor_1 (y[1], x[1], x[0]);
endmodule

module Exercicio03 (
  input  [2:0] x,
  input  [2:0] y,
  input  op,
  output [3:0] out_4,
  output carryOut,
  output [2:0] s
);

  Exercicio01 exercicio01_1 (.x(x), .y(y), .op(op), .carryOut(carryOut), .s(s));
  Inc1 inc1_1 (.x(s), .y(out_4));
endmodule
