// Logisim project Exemplo034.circ as structural Verilog: 8 circuits, main circuit main
module main (
  input  [3:0] a,
  input  [3:0] b,
  input  Carry_in,
  input  [3:0] declemento_de_1,
  output [4:0] Saida___overflow,
  output Saida_detector
);

  wire Selector_5_s, Somador_overflow, subtrator_1_sinal;
  wire [3:0] Selector_s, Somador_saida, subtrator_1_saida;

  Somador Somador (.a(a), .b(b), .Carry_in(Carry_in), .Overflow(Somador_overflow), .Saida(Somador_saida));
  Subtrator subtrator_1 (.a(a), .b(b), .Carrin_in(1'b0), .Sinal(subtrator_1_sinal), .saida(subtrator_1_saida));
  Selector Selector (.a(Somador_saida[0]), .b(subtrator_1_saida[0]), .selector(Carry_in), .s(Selector_s[0]));
  Selector Selector_2 (.a(Somador_saida[1]), .b(subtrator_1_saida[1]), .selector(Carry_in), .s(Selector_s[1]));
  Selector Selector_3 (.a(Somador_saida[2]), .b(subtrator_1_saida[2]), .selector(Carry_in), .s(Selector_s[2]));
  Selector Selector_4 (.a(Somador_saida[3]), .b(subtrator_1_saida[3]), .selector(Carry_in), .s(Selector_s[3]));
  Selector Selector_5 (.a(Somador_overflow), .b(subtrator_1_sinal), .selector(Carry_in), .s(Selector_5_s));
  Subtrator subtrator_2 (
    .a(Selector_s), .b(declemento_de_1), .Carrin_in(Selector_5_s), .Sinal(Saida___overflow[4]),
    .saida(Saida___overflow[3:0]));
  Detector_de_zero detector_de_zero_1 (.in_1(Selector_s), .out_2(Saida_detector));

  // Notes on the sheet:
  //   SIM=1 NAO=0
endmodule

module Selector (
  input  a,
  input  b,
  input  selector,
  output s
);

  wire and_1_out, and_2_out, not_1_out;

  not not_1 (not_1_out, selector);
  and and_1 (and_1_out, a, not_1_out);
  and and_2 (and_2_out, b, selector);
  or or_1 (s, and_1_out, and_2_out);
endmodule

module SubCircuitoSomador (
  input  a,
  input  b,
  input  entrada_overflow,
  output \output ,
  output outpu_overflow
);

  wire and_1_out, and_2_out, xor_1_out;

  xor xor_1 (xor_1_out, b, a);
  and and_1 (and_1_out, b, a);
  xor xor_2 (\output , xor_1_out, entrada_overflow);
  and and_2 (and_2_out, xor_1_out, entrada_overflow);
  or or_1 (outpu_overflow, and_2_out, and_1_out);
endmodule

module Subtrator (
  input  [3:0] a,
  input  [3:0] b,
  input  Carrin_in,
  output Sinal,
  output [3:0] saida
);

  wire subcircuitosubtrator_1_carry_on, subcircuitosubtrator_2_carry_on, subcircuitosubtrator_3_carry_on;

  SubCircuitoSubtrator subcircuitosubtrator_1 (
    .a(a[0]), .b(b[0]), .carry_in(Carrin_in), .saida(saida[0]), .carry_on(subcircuitosubtrator_1_carry_on));
  SubCircuitoSubtrator subcircuitosubtrator_2 (
    .a(a[1]), .b(b[1]), .carry_in(subcircuitosubtrator_1_carry_on), .saida(saida[1]),
    .carry_on(subcircuitosubtrator_2_carry_on));
  SubCircuitoSubtrator subcircuitosubtrator_3 (
    .a(a[2]), .b(b[2]), .carry_in(subcircuitosubtrator_2_carry_on), .saida(saida[2]),
    .carry_on(subcircuitosubtrator_3_carry_on));
  SubCircuitoSubtrator subcircuitosubtrator_4 (
    .a(a[3]), .b(b[3]), .carry_in(subcircuitosubtrator_3_carry_on), .saida(saida[3]), .carry_on(Sinal));
endmodule

module Somador (
  input  [3:0] a,
  input  [3:0] b,
  input  Carry_in,
  output Overflow,
  output [3:0] Saida
);

  wire subcircuitosomador_1_outpu_overflow, subcircuitosomador_2_outpu_overflow,
       subcircuitosomador_3_outpu_overflow;

  SubCircuitoSomador subcircuitosomador_1 (
    .entrada_overflow(Carry_in), .a(a[0]), .b(b[0]), .\output (Saida[0]),
    .outpu_overflow(subcircuitosomador_1_outpu_overflow));
  SubCircuitoSomador subcircuitosomador_2 (
    .entrada_overflow(subcircuitosomador_1_outpu_overflow), .a(a[1]), .b(b[1]), .\output (Saida[1]),
    .outpu_overflow(subcircuitosomador_2_outpu_overflow));
  SubCircuitoSomador subcircuitosomador_3 (
    .entrada_overflow(subcircuitosomador_2_outpu_overflow), .a(a[2]), .b(b[2]), .\output (Saida[2]),
    .outpu_overflow(subcircuitosomador_3_outpu_overflow));
  SubCircuitoSomador subcircuitosomador_4 (
    .entrada_overflow(subcircuitosomador_3_outpu_overflow), .a(a[3]), .b(b[3]), .\output (Saida[3]),
    .outpu_overflow(Overflow));

  // Notes on the sheet:
  //   Carry_in
  //   A
  //                  Saida 
  //   B
endmodule

module SubCircuitoSubtrator (
  input  a,
  input  b,
  input  carry_in,
  output saida,
  output carry_on
);

  wire a_xor_b_out, n_a___b_out, n_a_xor_b_____carry_in_out, n_a_xor_b_out, na_out;

  not na (na_out, a);
  xor a_xor_b (a_xor_b_out, a, b);
  and n_a___b (n_a___b_out, na_out, b);
  not n_a_xor_b (n_a_xor_b_out, a_xor_b_out);
  xor a_xor_b__xor__carry_in (saida, a_xor_b_out, carry_in);
  and n_a_xor_b_____carry_in (n_a_xor_b_____carry_in_out, n_a_xor_b_out, carry_in);
  or or_1 (carry_on, n_a___b_out, n_a_xor_b_____carry_in_out);
endmodule

module Detector_de_zero (
  input  [3:0] in_1,
  output out_2
);

  or or_1 (out_2, in_1[0], in_1[1], in_1[2], in_1[3]);
endmodule

module Inclemento_de_1 (
  input  [3:0] a,
  input  [3:0] complemento,
  input  Carry_in,
  output Overflow,
  output [3:0] saida
);

  wire subcircuitosomador_1_outpu_overflow, subcircuitosomador_2_outpu_overflow,
       subcircuitosomador_3_outpu_overflow;

  SubCircuitoSomador subcircuitosomador_1 (
    .entrada_overflow(Carry_in), .a(a[0]), .b(complemento[0]), .\output (saida[0]),
    .outpu_overflow(subcircuitosomador_1_outpu_overflow));
  SubCircuitoSomador subcircuitosomador_2 (
    .entrada_overflow(subcircuitosomador_1_outpu_overflow), .a(a[1]), .b(complemento[0]),
    .\output (saida[1]), .outpu_overflow(subcircuitosomador_2_outpu_overflow));
  SubCircuitoSomador subcircuitosomador_3 (
    .entrada_overflow(subcircuitosomador_2_outpu_overflow), .a(a[2]), .b(complemento[0]),
    .\output (saida[2]), .outpu_overflow(subcircuitosomador_3_outpu_overflow));
  SubCircuitoSomador subcircuitosomador_4 (
    .entrada_overflow(subcircuitosomador_3_outpu_overflow), .a(a[3]), .b(complemento[0]),
    .\output (saida[3]), .outpu_overflow(Overflow));
  // Pins of 1 and 4 bits meet at complemento
endmodule
