// Logisim project Exemplo35.circ as structural Verilog: 1 circuit, main circuit main
module main (
  input  in_1,
  input  in_2,
  input  in_3,
  input  in_4,
  output out_5,
  output out_6,
  output out_7
);

  wire and_1_out, and_2_out, and_3_out, and_4_out, not_1_out, not_2_out, not_3_out, not_4_out, xor_1_out,
       xor_2_out;

  not not_1 (not_1_out, in_1);
  not not_2 (not_2_out, in_2);
  not not_3 (not_3_out, in_3);
  not not_4 (not_4_out, in_4);
  xor xor_1 (xor_1_out, in_1, not_3_out);
  xor xor_2 (xor_2_out, in_2, not_4_out);
  and and_1 (and_1_out, in_1, not_3_out);
  and and_2 (and_2_out, xor_1_out, in_2, not_4_out);
  and and_3 (and_3_out, not_1_out, in_3);
  and and_4 (and_4_out, xor_1_out, not_2_out, in_4);
  and and_5 (out_5, xor_1_out, xor_2_out);
  or or_1 (out_6, and_1_out, and_2_out);
  or or_2 (out_7, and_3_out, and_4_out);

  // Notes on the sheet:
  //   a=b
  //   a>b
  //   a<b
endmodule
