// Logisim project Exercicios.circ as structural Verilog: 12 circuits, main circuit FullAdder
// FA
module FullAdder (
  input  a,
  input  b,
  input  c,
  output s1,
  output s0
);

  wire and_1_out, and_2_out, xor_1_out;

  xor xor_1 (xor_1_out, b, a);
  and and_1 (and_1_out, b, a);
  xor xor_2 (s1, c, xor_1_out);
  and and_2 (and_2_out, xor_1_out, c);
  or or_1 (s0, and_2_out, and_1_out);
endmodule

// HA
module HalfAdder (
  input  a,
  input  b,
  output s1,
  output s0
);

  xor xor_1 (s1, b, a);
  and and_1 (s0, b, a);
endmodule

// HS
module HalfSub (
  input  a,
  input  b,
  output s1,
  output s0
);

  xor xor_1 (s1, b, a);
  and and_1 (s0, b, ~a);  // AND_Gate
endmodule

// FS
module FullSub (
  input  c,
  input  a,
  input  b,
  output s1,
  output s0
);

  wire and_1_out, and_2_out, xor_1_out;

  xor xor_1 (xor_1_out, b, a);
  and and_1 (and_1_out, b, ~a);  // AND_Gate
  xor xor_2 (s1, c, xor_1_out);
  and and_2 (and_2_out, c, ~xor_1_out);  // AND_Gate
  or or_1 (s0, and_2_out, and_1_out);
endmodule

// 0Flag
module ZeroFlag (
  input  in_1,
  input  [2:0] in_2,
  output out_3
);

  nor nor_1 (out_3, in_1, in_2[0], in_2[1], in_2[2]);
endmodule

module Inc1 (
  input  [2:0] x,
  output [3:0] s
);

  wire and_2_out, and_3_out, and_4_out, not_1_out, not_2_out, not_3_out;

  not not_1 (not_1_out, x[2]);
  not not_2 (not_2_out, x[1]);
  not not_3 (not_3_out, x[0]);
  not not_4 (s[0], x[0]);
  and and_1 (s[3], x[2], x[1], x[0]);
  and and_2 (and_2_out, not_1_out, x[1], x[0]);
  and and_3 (and_3_out, x[2], not_2_out);
  and and_4 (and_4_out, x[2], not_3_out);
  or or_1 (s[2], and_2_out, and_3_out, and_4_out);
  xor xor_1 (s[1], x[1], x[0]);
endmodule

module Dec1 (
  input  [2:0] x,
  output [3:0] s
);

  wire and_2_out, and_3_out, not_1_out, not_2_out, not_3_out, not_4_out, not_5_out, not_6_out, or_1_out;

  not not_1 (not_1_out, x[2]);
  not not_2 (not_2_out, x[1]);
  not not_3 (not_3_out, x[0]);
  not not_4 (not_4_out, x[2]);
  not not_5 (not_5_out, x[1]);
  not not_6 (not_6_out, x[0]);
  or or_1 (or_1_out, x[1], x[0]);
  not not_7 (s[0], x[0]);
  and and_1 (s[3], not_1_out, not_2_out, not_3_out);
  and and_2 (and_2_out, not_4_out, not_5_out, not_6_out);
  and and_3 (and_3_out, x[2], or_1_out);
  xnor xnor_1 (s[1], x[1], x[0]);
  or or_2 (s[2], and_2_out, and_3_out);
endmodule

// SA
module Exercicio01 (
  input  [2:0] x,
  input  [2:0] y,
  input  op,
  output carryOut,
  output [2:0] s
);

  wire fulladder_1_s0, fulladder_2_s0, fulladder_3_s0, xor_1_out, xor_3_out, xor_4_out;

  xor xor_1 (xor_1_out, op, y[2]);
  FullAdder fulladder_1 (.s1(s[2]), .s0(fulladder_1_s0), .a(xor_1_out), .b(x[2]), .c(fulladder_2_s0));
  xor xor_2 (carryOut, op, fulladder_1_s0);
  xor xor_3 (xor_3_out, op, y[1]);
  FullAdder fulladder_2 (.s1(s[1]), .s0(fulladder_2_s0), .a(xor_3_out), .b(x[1]), .c(fulladder_3_s0));
  xor xor_4 (xor_4_out, y[0], op);
  FullAdder fulladder_3 (.s1(s[0]), .s0(fulladder_3_s0), .a(xor_4_out), .b(x[0]), .c(op));
endmodule

module Exercicio02 (
  input  [2:0] x,
  input  [2:0] y,
  input  op,
  output out_4,
  output carryOut,
  output [2:0] s
);

  Exercicio01 exercicio01_1 (.x(x), .y(y), .op(op), .carryOut(carryOut), .s(s));
  ZeroFlag zeroflag_1 (.in_1(carryOut), .in_2(s), .out_3(out_4));
endmodule

module Exercicio03 (
  input  [2:0] x,
  input  [2:0] y,
  input  op,
  output [3:0] out_4,
  output out_5,
  output carryOut,
  output [2:0] s
);

  Inc1 inc1_1 (.x(x), .s(out_4));
  Exercicio01 exercicio01_1 (.x(x), .y(y), .op(op), .carryOut(carryOut), .s(s));
  ZeroFlag zeroflag_1 (.in_1(carryOut), .in_2(s), .out_3(out_5));

  // Notes on the sheet:
  //   incremento de 1 de x
endmodule

module Exercicio06 (
  input  [2:0] x,
  input  [2:0] y,
  input  op,
  output [3:0] out_4,
  output out_5,
  output carryOut,
  output [2:0] s
);

  Dec1 dec1_1 (.x(x), .s(out_4));
  Exercicio01 exercicio01_1 (.x(x), .y(y), .op(op), .carryOut(carryOut), .s(s));
  ZeroFlag zeroflag_1 (.in_1(carryOut), .in_2(s), .out_3(out_5));

  // Notes on the sheet:
  //   decremento de 1 de x
endmodule

module Exercicio07 (
  input  a,
  input  b,
  input  c,
  input  d,
  input  e,
  input  f,
  output maior,
  output igual,
  output menor
);

  wire and_1_out, and_2_out, and_3_out, and_4_out, and_5_out, and_6_out, and_7_out, and_8_out, and_9_out,
       and_10_out, and_11_out, and_12_out, and_13_out, and_14_out, and_15_out, and_16_out, and_17_out,
       and_18_out, and_19_out, and_20_out, and_21_out, and_22_out, not_1_out, not_2_out, not_3_out,
       not_4_out, not_5_out, not_6_out, not_7_out, not_8_out, not_9_out, not_10_out, not_11_out, not_12_out,
       not_13_out, not_14_out, not_15_out, not_16_out, not_17_out, not_18_out, not_19_out, not_20_out,
       not_21_out, not_22_out, not_23_out, not_24_out, not_25_out, not_26_out, not_27_out, not_28_out,
       not_29_out, not_30_out, not_31_out, not_32_out, not_33_out, not_34_out, not_35_out, not_36_out,
       not_37_out, not_38_out, not_39_out, not_40_out, not_41_out, not_42_out, not_43_out, not_44_out,
       not_45_out, not_46_out, not_47_out, not_48_out;

  not not_1 (not_1_out, d);
  not not_2 (not_2_out, e);
  not not_3 (not_3_out, f);
  not not_4 (not_4_out, d);
  not not_5 (not_5_out, e);
  not not_6 (not_6_out, d);
  not not_7 (not_7_out, f);
  not not_8 (not_8_out, d);
  not not_9 (not_9_out, e);
  not not_10 (not_10_out, f);
  not not_11 (not_11_out, e);
  not not_12 (not_12_out, f);
  not not_13 (not_13_out, a);
  not not_14 (not_14_out, b);
  not not_15 (not_15_out, c);
  not not_16 (not_16_out, d);
  not not_17 (not_17_out, e);
  not not_18 (not_18_out, f);
  not not_19 (not_19_out, a);
  not not_20 (not_20_out, b);
  not not_21 (not_21_out, d);
  not not_22 (not_22_out, e);
  not not_23 (not_23_out, a);
  not not_24 (not_24_out, c);
  not not_25 (not_25_out, d);
  not not_26 (not_26_out, f);
  not not_27 (not_27_out, a);
  not not_28 (not_28_out, d);
  not not_29 (not_29_out, b);
  not not_30 (not_30_out, c);
  not not_31 (not_31_out, e);
  not not_32 (not_32_out, f);
  not not_33 (not_33_out, b);
  not not_34 (not_34_out, e);
  not not_35 (not_35_out, c);
  not not_36 (not_36_out, f);
  not not_37 (not_37_out, a);
  not not_38 (not_38_out, b);
  not not_39 (not_39_out, c);
  not not_40 (not_40_out, a);
  not not_41 (not_41_out, b);
  not not_42 (not_42_out, a);
  not not_43 (not_43_out, c);
  not not_44 (not_44_out, a);
  not not_45 (not_45_out, b);
  not not_46 (not_46_out, c);
  not not_47 (not_47_out, b);
  not not_48 (not_48_out, c);
  and and_1 (and_1_out, c, not_1_out, not_2_out, not_3_out);
  and and_2 (and_2_out, b, not_4_out, not_5_out);
  and and_3 (and_3_out, b, c, not_6_out, not_7_out);
  and and_4 (and_4_out, a, not_8_out);
  and and_5 (and_5_out, a, c, not_9_out, not_10_out);
  and and_6 (and_6_out, a, b, not_11_out);
  and and_7 (and_7_out, a, b, c, not_12_out);
  and and_8 (and_8_out, not_13_out, not_14_out, not_15_out, not_16_out, not_17_out, not_18_out);
  and and_9 (and_9_out, not_19_out, not_20_out, c, not_21_out, not_22_out, f);
  and and_10 (and_10_out, not_23_out, b, not_24_out, not_25_out, e, not_26_out);
  and and_11 (and_11_out, not_27_out, b, c, not_28_out, e, f);
  and and_12 (and_12_out, a, not_29_out, not_30_out, d, not_31_out, not_32_out);
  and and_13 (and_13_out, a, not_33_out, c, d, not_34_out, f);
  and and_14 (and_14_out, a, b, not_35_out, d, e, not_36_out);
  and and_15 (and_15_out, a, b, c, d, e, f);
  and and_16 (and_16_out, not_37_out, not_38_out, not_39_out, f);
  and and_17 (and_17_out, not_40_out, not_41_out, e);
  and and_18 (and_18_out, not_42_out, not_43_out, e, f);
  and and_19 (and_19_out, not_44_out, d);
  and and_20 (and_20_out, not_45_out, not_46_out, d, f);
  and and_21 (and_21_out, not_47_out, d, e);
  and and_22 (and_22_out, not_48_out, d, e, f);
  or or_1 (maior, and_1_out, and_2_out, and_3_out, and_4_out, and_5_out, and_6_out, and_7_out);
  or or_2 (igual, and_8_out, and_9_out, and_10_out, and_11_out, and_12_out, and_13_out, and_14_out, and_15_out);
  or or_3 (menor, and_16_out, and_17_out, and_18_out, and_19_out, and_20_out, and_21_out, and_22_out);
endmodule
