// Logisim project Guia05.circ as structural Verilog: 9 circuits, main circuit main
module main (
  input  [2:0] a,
  input  [2:0] b,
  input  Carry_in,
  output Carry_out,
  output [2:0] out_5
);

  wire fu_1_out_5, fu_2_out_5, fu_3_out_5, xor_2_out, xor_3_out, xor_4_out;

  xor xor_1 (Carry_out, Carry_in, fu_1_out_5);
  xor xor_2 (xor_2_out, b[2], Carry_in);
  FU fu_1 (.out_5(fu_1_out_5), .in_1(a[2]), .in_2(xor_2_out), .out_4(out_5[2]), .in_3(fu_2_out_5));
  xor xor_3 (xor_3_out, b[1], Carry_in);
  FU fu_2 (.out_5(fu_2_out_5), .in_1(a[1]), .in_2(xor_3_out), .out_4(out_5[1]), .in_3(fu_3_out_5));
  xor xor_4 (xor_4_out, b[0], Carry_in);
  FU fu_3 (.out_5(fu_3_out_5), .in_1(a[0]), .in_2(xor_4_out), .out_4(out_5[0]), .in_3(Carry_in));
endmodule

module HA (
  input  a,
  input  b,
  output s0,
  output s1
);

  xor xor_1 (s0, a, b);
  and and_1 (s1, a, b);
endmodule

module FU (
  input  in_1,
  input  in_2,
  input  in_3,
  output out_4,
  output out_5
);

  wire ha_1_s0, ha_1_s1, ha_2_s1;

  HA ha_1 (.a(in_1), .b(in_2), .s0(ha_1_s0), .s1(ha_1_s1));
  or or_1 (out_5, ha_1_s1, ha_2_s1);
  HA ha_2 (.a(ha_1_s0), .b(in_3), .s0(out_4), .s1(ha_2_s1));
endmodule

module Exemplo031 (
  input  [2:0] a,
  input  [2:0] b,
  input  Carry_in,
  output Carry_out,
  output [2:0] out_5
);

  wire fu_1_out_5, fu_2_out_5, fu_3_out_5, xor_2_out, xor_3_out, xor_4_out;

  xor xor_1 (Carry_out, Carry_in, fu_1_out_5);
  xor xor_2 (xor_2_out, b[2], Carry_in);
  FU fu_1 (.out_5(fu_1_out_5), .in_1(a[2]), .in_2(xor_2_out), .out_4(out_5[2]), .in_3(fu_2_out_5));
  xor xor_3 (xor_3_out, b[1], Carry_in);
  FU fu_2 (.out_5(fu_2_out_5), .in_1(a[1]), .in_2(xor_3_out), .out_4(out_5[1]), .in_3(fu_3_out_5));
  xor xor_4 (xor_4_out, b[0], Carry_in);
  FU fu_3 (.out_5(fu_3_out_5), .in_1(a[0]), .in_2(xor_4_out), .out_4(out_5[0]), .in_3(Carry_in));
endmodule

module Exemplo032 (
  input  [2:0] in_1,
  input  [2:0] in_2,
  input  in_3,
  output out_4,
  output [2:0] out_5,
  output out_6
);

  wire fu_1_out_5, fu_2_out_5, fu_3_out_5, xor_2_out, xor_3_out, xor_4_out;

  xor xor_1 (out_4, in_3, fu_1_out_5);
  xor xor_2 (xor_2_out, in_2[2], in_3);
  FU fu_1 (.out_5(fu_1_out_5), .in_1(in_1[2]), .in_2(xor_2_out), .out_4(out_5[2]), .in_3(fu_2_out_5));
  xor xor_3 (xor_3_out, in_2[1], in_3);
  FU fu_2 (.out_5(fu_2_out_5), .in_1(in_1[1]), .in_2(xor_3_out), .out_4(out_5[1]), .in_3(fu_3_out_5));
  xor xor_4 (xor_4_out, in_2[0], in_3);
  FU fu_3 (.out_5(fu_3_out_5), .in_1(in_1[0]), .in_2(xor_4_out), .out_4(out_5[0]), .in_3(in_3));
  nor nor_1 (out_6, out_4, out_5[2], out_5[1], out_5[0]);
endmodule

module Exemplo033 (
  input  [2:0] in_1,
  input  [2:0] in_2,
  input  in_3,
  output out_4,
  output [2:0] out_5,
  output out_6
);

  wire fu_1_out_5, fu_2_out_5, fu_3_out_5, xor_2_out, xor_3_out, xor_4_out;

  xor xor_1 (out_4, in_3, fu_1_out_5);
  xor xor_2 (xor_2_out, in_2[2], in_3);
  FU fu_1 (.out_5(fu_1_out_5), .in_1(in_1[2]), .in_2(xor_2_out), .out_4(out_5[2]), .in_3(fu_2_out_5));
  xor xor_3 (xor_3_out, in_2[1], in_3);
  FU fu_2 (.out_5(fu_2_out_5), .in_1(in_1[1]), .in_2(xor_3_out), .out_4(out_5[1]), .in_3(fu_3_out_5));
  xor xor_4 (xor_4_out, in_2[0], in_3);
  FU fu_3 (.out_5(fu_3_out_5), .in_1(in_1[0]), .in_2(xor_4_out), .out_4(out_5[0]), .in_3(1'b1));
  nor nor_1 (out_6, out_4, out_5[2], out_5[1], out_5[0]);
endmodule

module Exemplo034 (
  input  [2:0] in_1,
  input  [2:0] in_2,
  input  in_3,
  output out_4,
  output [2:0] out_5,
  output out_6
);

  wire fu_1_out_5, fu_2_out_5, fu_3_out_5, not_1_out, xor_2_out, xor_3_out, xor_4_out;

  xor xor_1 (out_4, in_3, fu_1_out_5);
  xor xor_2 (xor_2_out, in_2[2], in_3);
  FU fu_1 (.out_5(fu_1_out_5), .in_1(in_1[2]), .in_2(xor_2_out), .out_4(out_5[2]), .in_3(fu_2_out_5));
  xor xor_3 (xor_3_out, in_2[1], in_3);
  FU fu_2 (.out_5(fu_2_out_5), .in_1(in_1[1]), .in_2(xor_3_out), .out_4(out_5[1]), .in_3(fu_3_out_5));
  xor xor_4 (xor_4_out, in_2[0], in_3);
  FU fu_3 (.out_5(fu_3_out_5), .in_1(in_1[0]), .in_2(xor_4_out), .out_4(out_5[0]), .in_3(not_1_out));
  not not_1 (not_1_out, 1'b1);
  nor nor_1 (out_6, out_4, out_5[2], out_5[1], out_5[0]);
endmodule

module CO (
  input  a,
  input  b,
  input  c0,
  input  c1,
  output s0,
  output s1
);

  wire and_1_out, and_2_out, and_3_out, and_4_out, not_1_out, not_2_out;

  not not_1 (not_1_out, b);
  not not_2 (not_2_out, a);
  or or_1 (s0, c0, and_1_out);
  and and_1 (and_1_out, not_1_out, a, c1);
  and and_2 (and_2_out, not_1_out, not_2_out, c1);
  and and_3 (and_3_out, b, a, c1);
  or or_2 (s1, and_2_out, and_3_out, and_4_out);
  and and_4 (and_4_out, c0, c1);
endmodule

module Exemplo035 (
  input  [2:0] a,
  input  [2:0] b,
  output [2:0] out_3
);

  wire co_1_s0, co_1_s1, co_2_s0, co_2_s1, not_1_out, not_2_out;

  not not_1 (not_1_out, a[2]);
  not not_2 (not_2_out, b[2]);
  CO co_1 (.c0(1'b0), .c1(1'b1), .a(not_1_out), .b(not_2_out), .s0(co_1_s0), .s1(co_1_s1));
  CO co_2 (.c0(co_1_s0), .c1(co_1_s1), .a(a[1]), .b(b[1]), .s0(co_2_s0), .s1(co_2_s1));
  CO co_3 (.c0(co_2_s0), .c1(co_2_s1), .a(a[0]), .b(b[0]), .s0(out_3[0]), .s1(out_3[1]));
  xnor xnor_1 (out_3[2], out_3[1], out_3[0]);
endmodule
