// Logisim project Circuitos.circ as structural Verilog: 8 circuits, main circuit Exemplo0031
module Exemplo0031 (
  input  [2:0] b,
  input  [2:0] a,
  input  carry_in,
  output carry_out,
  output [2:0] s
);

  wire somador_completo_1_carry_out, somador_completo_2_carry_out, somador_completo_3_carry_out, xor_2_out,
       xor_3_out, xor_4_out;

  xor xor_1 (carry_out, carry_in, somador_completo_1_carry_out);
  xor xor_2 (xor_2_out, carry_in, b[2]);
  somador_completo somador_completo_1 (
    .carry_out(somador_completo_1_carry_out), .a(a[2]), .b(xor_2_out), .s(s[2]),
    .carry_in(somador_completo_2_carry_out));
  xor xor_3 (xor_3_out, carry_in, b[1]);
  somador_completo somador_completo_2 (
    .carry_out(somador_completo_2_carry_out), .a(a[1]), .b(xor_3_out), .s(s[1]),
    .carry_in(somador_completo_3_carry_out));
  xor xor_4 (xor_4_out, carry_in, b[0]);
  somador_completo somador_completo_3 (
    .carry_out(somador_completo_3_carry_out), .a(a[0]), .b(xor_4_out), .s(s[0]), .carry_in(carry_in));
endmodule

module Exemplo0032 (
  input  [2:0] b,
  input  [2:0] a,
  input  carry_in,
  output carry_out,
  output [2:0] s,
  output flag
);

  wire somador_completo_1_carry_out, somador_completo_2_carry_out, somador_completo_3_carry_out, xor_2_out,
       xor_3_out, xor_4_out;

  xor xor_1 (carry_out, carry_in, somador_completo_1_carry_out);
  xor xor_2 (xor_2_out, carry_in, b[2]);
  somador_completo somador_completo_1 (
    .carry_out(somador_completo_1_carry_out), .a(a[2]), .b(xor_2_out), .s(s[2]),
    .carry_in(somador_completo_2_carry_out));
  xor xor_3 (xor_3_out, carry_in, b[1]);
  somador_completo somador_completo_2 (
    .carry_out(somador_completo_2_carry_out), .a(a[1]), .b(xor_3_out), .s(s[1]),
    .carry_in(somador_completo_3_carry_out));
  xor xor_4 (xor_4_out, carry_in, b[0]);
  somador_completo somador_completo_3 (
    .carry_out(somador_completo_3_carry_out), .a(a[0]), .b(xor_4_out), .s(s[0]), .carry_in(carry_in));
  nor nor_1 (flag, s[2], s[1], s[0]);
endmodule

module Exemplo0033 (
  input  [2:0] b,
  input  [2:0] a,
  input  carry_in,
  output carry_out,
  output [2:0] s,
  output flag
);

  wire somador_completo_1_carry_out, somador_completo_2_carry_out, somador_completo_3_carry_out, xor_2_out,
       xor_3_out, xor_4_out;
  wire [2:0] incremento_1_s;

  xor xor_1 (carry_out, carry_in, somador_completo_1_carry_out);
  incremento incremento_1 (.a(a), .s(incremento_1_s));  // open: out_2
  xor xor_2 (xor_2_out, carry_in, b[2]);
  somador_completo somador_completo_1 (
    .carry_out(somador_completo_1_carry_out), .a(incremento_1_s[2]), .b(xor_2_out), .s(s[2]),
    .carry_in(somador_completo_2_carry_out));
  xor xor_3 (xor_3_out, carry_in, b[1]);
  somador_completo somador_completo_2 (
    .carry_out(somador_completo_2_carry_out), .a(incremento_1_s[1]), .b(xor_3_out), .s(s[1]),
    .carry_in(somador_completo_3_carry_out));
  xor xor_4 (xor_4_out, carry_in, b[0]);
  somador_completo somador_completo_3 (
    .carry_out(somador_completo_3_carry_out), .a(incremento_1_s[0]), .b(xor_4_out), .s(s[0]),
    .carry_in(carry_in));
  nor nor_1 (flag, s[2], s[1], s[0]);
endmodule

module Exemplo0034 (
  input  [2:0] b,
  input  [2:0] a,
  input  carry_in,
  output overflow,
  output [2:0] s,
  output flag
);

  wire somador_completo_1_carry_out, somador_completo_2_carry_out, somador_completo_3_carry_out, xor_2_out,
       xor_3_out, xor_4_out;
  wire [2:0] incremento_1_s;

  xor xor_1 (overflow, carry_in, somador_completo_1_carry_out);
  incremento incremento_1 (.a(a), .s(incremento_1_s));  // open: out_2
  xor xor_2 (xor_2_out, carry_in, b[2]);
  somador_completo somador_completo_1 (
    .carry_out(somador_completo_1_carry_out), .a(incremento_1_s[2]), .b(xor_2_out), .s(s[2]),
    .carry_in(somador_completo_2_carry_out));
  xor xor_3 (xor_3_out, carry_in, b[1]);
  somador_completo somador_completo_2 (
    .carry_out(somador_completo_2_carry_out), .a(incremento_1_s[1]), .b(xor_3_out), .s(s[1]),
    .carry_in(somador_completo_3_carry_out));
  xor xor_4 (xor_4_out, carry_in, b[0]);
  somador_completo somador_completo_3 (
    .carry_out(somador_completo_3_carry_out), .a(incremento_1_s[0]), .b(xor_4_out), .s(s[0]),
    .carry_in(carry_in));
  nor nor_1 (flag, s[2], s[1], s[0]);
endmodule

module Exemplo0035 (
  input  [2:0] b,
  input  [2:0] a,
  input  carry_in,
  output overflow,
  output _0_plus,
  output [2:0] s,
  output flag
);

  wire somador_completo_1_carry_out, somador_completo_2_carry_out, somador_completo_3_carry_out, xor_2_out,
       xor_3_out, xor_4_out;
  wire [2:0] incremento_1_s;

  xor xor_1 (overflow, carry_in, somador_completo_1_carry_out);
  incremento incremento_1 (.a(a), .s(incremento_1_s));  // open: out_2
  xor xor_2 (xor_2_out, carry_in, b[2]);
  somador_completo somador_completo_1 (
    .carry_out(somador_completo_1_carry_out), .a(incremento_1_s[2]), .b(xor_2_out), .s(_0_plus),
    .carry_in(somador_completo_2_carry_out));
  xor xor_3 (xor_3_out, carry_in, b[1]);
  somador_completo somador_completo_2 (
    .carry_out(somador_completo_2_carry_out), .a(incremento_1_s[1]), .b(xor_3_out), .s(s[1]),
    .carry_in(somador_completo_3_carry_out));
  xor xor_4 (xor_4_out, carry_in, b[0]);
  somador_completo somador_completo_3 (
    .carry_out(somador_completo_3_carry_out), .a(incremento_1_s[0]), .b(xor_4_out), .s(s[0]),
    .carry_in(carry_in));
  nor nor_1 (flag, _0_plus, s[1], s[0]);

  assign s[2] = _0_plus;

  // Notes on the sheet:
  //   1-minus
endmodule

// HA
module meia_soma (
  input  a,
  input  b,
  output s,
  output carry_out
);

  xor XOR (s, a, b);
  and AND (carry_out, b, a);
endmodule

// FA
module somador_completo (
  input  a,
  input  b,
  input  carry_in,
  output carry_out,
  output s
);

  wire meia_soma_1_carry_out, meia_soma_1_s, meia_soma_2_carry_out;

  meia_soma meia_soma_1 (.a(a), .b(b), .s(meia_soma_1_s), .carry_out(meia_soma_1_carry_out));
  meia_soma meia_soma_2 (.a(carry_in), .b(meia_soma_1_s), .s(s), .carry_out(meia_soma_2_carry_out));
  or OR (carry_out, meia_soma_2_carry_out, meia_soma_1_carry_out);
endmodule

// inc1
module incremento (
  input  [2:0] a,
  output out_2,
  output [2:0] s
);

  Exemplo0031 exemplo0031_1 (.carry_out(out_2), .a(a), .b(3'b001), .s(s), .carry_in(1'b0));
endmodule
