// Logisim project Exercicio0031.circ as structural Verilog: 4 circuits, main circuit main
module main (
  input  Carry_in,
  input  a0,
  input  a1,
  input  Sinal_a,
  input  b0,
  input  b1,
  input  Sinal_b,
  output out_8,
  output out_9,
  output out_10,
  output out_11
);

  wire complemento1_1_out_3, complemento1_2_out_3, complemento1_3_out_3, fulladder_1_out_5,
       fulladder_2_out_5, fulladder_3_out_5;

  Complemento1 complemento1_1 (.in_1(b0), .in_2(Carry_in), .out_3(complemento1_1_out_3));
  Complemento1 complemento1_2 (.in_1(b1), .in_2(Carry_in), .out_3(complemento1_2_out_3));
  Complemento1 complemento1_3 (.in_1(Sinal_b), .in_2(Carry_in), .out_3(complemento1_3_out_3));
  FullAdder fulladder_1 (
    .in_2(a0), .in_3(complemento1_1_out_3), .in_1(Carry_in), .out_5(fulladder_1_out_5), .out_4(out_11));
  FullAdder fulladder_2 (
    .in_2(a1), .in_3(complemento1_2_out_3), .in_1(fulladder_1_out_5), .out_5(fulladder_2_out_5),
    .out_4(out_10));
  FullAdder fulladder_3 (
    .in_2(Sinal_a), .in_3(complemento1_3_out_3), .in_1(fulladder_2_out_5), .out_5(fulladder_3_out_5),
    .out_4(out_9));
  Complemento1 complemento1_4 (.in_1(fulladder_3_out_5), .in_2(Carry_in), .out_3(out_8));

  // Notes on the sheet:
  //   Guia 05 - Exercício0031
  //   Lucas Cardoso - 441694
  //   C1
  //   C1
  //   C1
  //   FA
  //   FA
  //   FA
  //   C1
endmodule

module HalfAdder (
  input  in_1,
  input  in_2,
  output out_3,
  output out_4
);

  xor XOR (out_3, in_1, in_2);
  and AND (out_4, in_1, in_2);
endmodule

module FullAdder (
  input  in_1,
  input  in_2,
  input  in_3,
  output out_4,
  output out_5
);

  wire HA_2_out_4, HA_out_3, HA_out_4;

  HalfAdder HA (.in_1(in_2), .in_2(in_3), .out_3(HA_out_3), .out_4(HA_out_4));
  HalfAdder HA_2 (.in_1(in_1), .in_2(HA_out_3), .out_3(out_4), .out_4(HA_2_out_4));
  xor XOR (out_5, HA_out_4, HA_2_out_4);
endmodule

module Complemento1 (
  input  in_1,
  input  in_2,
  output out_3
);

  xor XOR (out_3, in_1, in_2);
endmodule
