// Logisim project Exercicio0033.circ as structural Verilog: 4 circuits, main circuit main
module main (
  input  Carry_in,
  input  a0,
  input  a1,
  input  Sinal_a,
  input  b0,
  input  b1,
  input  Sinal_b,
  output out_8,
  output out_9,
  output out_10,
  output out_11
);

  wire fulladder_1_out_4, fulladder_1_out_5, fulladder_2_out_4, fulladder_2_out_5, fulladder_3_out_5;

  FullAdder fulladder_1 (.in_2(a0), .in_3(b0), .in_1(Carry_in), .out_5(fulladder_1_out_5), .out_4(fulladder_1_out_4));
  FullAdder fulladder_2 (
    .in_2(a1), .in_3(b1), .in_1(fulladder_1_out_5), .out_5(fulladder_2_out_5), .out_4(fulladder_2_out_4));
  FullAdder fulladder_3 (
    .in_2(Sinal_a), .in_3(Sinal_b), .in_1(fulladder_2_out_5), .out_5(fulladder_3_out_5), .out_4(out_8));
  Incremento1 incremento1_1 (
    .in_1(fulladder_1_out_4), .in_2(fulladder_2_out_4), .out_4(out_9), .out_5(out_10), .out_6(out_11),
    .in_3(fulladder_3_out_5));

  // Notes on the sheet:
  //   Guia 05 - Exercício0033
  //   Lucas Cardoso - 441694
  //   FA
  //   FA
  //   FA
  //   i1
endmodule

module HalfAdder (
  input  in_1,
  input  in_2,
  output out_3,
  output out_4
);

  xor XOR (out_3, in_1, in_2);
  and AND (out_4, in_1, in_2);
endmodule

module FullAdder (
  input  in_1,
  input  in_2,
  input  in_3,
  output out_4,
  output out_5
);

  wire HA_2_out_4, HA_out_3, HA_out_4;

  HalfAdder HA (.in_1(in_2), .in_2(in_3), .out_3(HA_out_3), .out_4(HA_out_4));
  HalfAdder HA_2 (.in_1(in_1), .in_2(HA_out_3), .out_3(out_4), .out_4(HA_2_out_4));
  xor XOR (out_5, HA_out_4, HA_2_out_4);
endmodule

module Incremento1 (
  input  in_1,
  input  in_2,
  input  in_3,
  output out_4,
  output out_5,
  output out_6
);

  wire fulladder_1_out_5;

  FullAdder fulladder_1 (.in_2(in_1), .in_3(1'b1), .in_1(in_3), .out_5(fulladder_1_out_5), .out_4(out_6));
  FullAdder fulladder_2 (.in_2(in_2), .in_3(1'b0), .in_1(fulladder_1_out_5), .out_5(out_4), .out_4(out_5));

  // Notes on the sheet:
  //   FA
  //   FA
endmodule
