// Logisim project Exemplo0035.circ as structural Verilog: 4 circuits, main circuit AU
module MenorMaiorIgual (
  input  [2:0] in_1,
  input  [2:0] in_2,
  output [2:0] out_3,
  output Igual,
  output [1:0] out_5
);

  wire not_1_out;

  not not_1 (not_1_out, out_5[1]);
  xor xor_1 (out_5[0], not_1_out, Igual);
  AU au_1 (
    .in_1(in_1), .in_2(in_2), .Sinal(out_5[1]), .out_8(out_3), .ZERO_FLAG(Igual));  // open: Overflow, c1_c2, Carry
endmodule

module AU (
  input  [2:0] in_1,
  input  [2:0] in_2,
  output [1:0] c1_c2,
  output Overflow,
  output ZERO_FLAG,
  output Carry,
  output Sinal,
  output [2:0] out_8
);

  wire adder_1_out_5, adder_2_out_5, adder_3_out_5, and_3_out, or_2_out, xor_2_out, xor_3_out, xor_4_out;

  or or_1 (Overflow, c1_c2[1], and_3_out);
  and and_1 (c1_c2[0], in_2[0], in_1[0]);
  and and_2 (c1_c2[1], in_2[1], in_1[1]);
  or or_2 (or_2_out, in_2[1], in_1[1]);
  and and_3 (and_3_out, c1_c2[0], or_2_out);
  xor xor_1 (Carry, 1'b1, adder_1_out_5);
  xor xor_2 (xor_2_out, in_2[2], 1'b1);
  Adder adder_1 (.in_1(adder_2_out_5), .in_2(in_1[2]), .in_3(xor_2_out), .out_4(out_8[2]), .out_5(adder_1_out_5));
  buf buffer_1 (Sinal, out_8[2]);
  xor xor_3 (xor_3_out, in_2[1], 1'b1);
  Adder adder_2 (.in_1(adder_3_out_5), .in_2(in_1[1]), .in_3(xor_3_out), .out_4(out_8[1]), .out_5(adder_2_out_5));
  xor xor_4 (xor_4_out, in_2[0], 1'b1);
  nor nor_1 (ZERO_FLAG, out_8[0], out_8[1], out_8[2]);
  Adder adder_3 (.in_1(1'b1), .in_2(in_1[0]), .in_3(xor_4_out), .out_4(out_8[0]), .out_5(adder_3_out_5));
endmodule

module Adder (
  input  in_1,
  input  in_2,
  input  in_3,
  output out_4,
  output out_5
);

  wire and_1_out, and_2_out, xor_1_out;

  xor xor_1 (xor_1_out, in_1, in_2);
  xor xor_2 (out_4, xor_1_out, in_3);
  and and_1 (and_1_out, in_3, xor_1_out);
  and and_2 (and_2_out, in_2, in_1);
  or or_1 (out_5, and_1_out, and_2_out);
endmodule

module Full_Adder (
  input  in_1,
  input  in_2,
  input  in_3,
  input  in_4,
  input  in_5,
  input  in_6,
  input  in_7,
  output out_8,
  output out_9,
  output out_10,
  output out_11
);

  wire adder_1_out_5, adder_2_out_5;

  Adder adder_1 (.in_1(in_1), .in_2(in_2), .in_3(in_3), .out_4(out_8), .out_5(adder_1_out_5));
  Adder adder_2 (.in_1(in_4), .in_2(in_5), .in_3(adder_1_out_5), .out_4(out_9), .out_5(adder_2_out_5));
  Adder adder_3 (.in_1(in_6), .in_2(in_7), .in_3(adder_2_out_5), .out_4(out_10), .out_5(out_11));
endmodule
