// Logisim project guia5.circ as structural Verilog: 5 circuits, main circuit soma completa
// FA
module soma_completa (
  input  vai_um,
  input  x,
  input  y,
  output s0,
  output s1___vai_um
);

  wire and_1_out, and_2_out, xor_1_out;

  xor xor_1 (xor_1_out, x, y);
  and and_1 (and_1_out, y, x);
  xor xor_2 (s0, vai_um, xor_1_out);
  and and_2 (and_2_out, xor_1_out, vai_um);
  or or_1 (s1___vai_um, and_2_out, and_1_out);
endmodule

// SUB
module diferenca_completa (
  input  vem_um,
  input  X,
  input  Y,
  output S0,
  output S1
);

  wire and_1_out, and_2_out, not_1_out, not_2_out, xor_1_out;

  not not_1 (not_1_out, X);
  xor xor_1 (xor_1_out, X, Y);
  and and_1 (and_1_out, Y, not_1_out);
  not not_2 (not_2_out, xor_1_out);
  xor xor_2 (S0, vem_um, xor_1_out);
  and and_2 (and_2_out, vem_um, not_2_out);
  or or_1 (S1, and_2_out, and_1_out);
endmodule

// Ig
module Comparador_igual (
  input  [2:0] in_1,
  input  [2:0] in_2,
  output out_3
);

  wire xnor_1_out, xnor_2_out, xnor_3_out;

  xnor xnor_1 (xnor_1_out, in_1[0], in_2[0]);
  xnor xnor_2 (xnor_2_out, in_1[1], in_2[1]);
  xnor xnor_3 (xnor_3_out, in_1[2], in_2[2]);
  and and_1 (out_3, xnor_1_out, xnor_2_out, xnor_3_out);
endmodule

module Exemplo0031 (
  input  [2:0] x,
  input  [2:0] y,
  input  carryIn,
  output [2:0] out_4,
  output out_5
);

  wire soma_completa_1_s1___vai_um, soma_completa_2_s1___vai_um, soma_completa_3_s1___vai_um, xor_2_out,
       xor_3_out, xor_4_out;

  xor xor_1 (out_5, carryIn, soma_completa_1_s1___vai_um);
  xor xor_2 (xor_2_out, y[2], carryIn);
  soma_completa soma_completa_1 (
    .vai_um(soma_completa_2_s1___vai_um), .x(x[2]), .y(xor_2_out), .s0(out_4[2]),
    .s1___vai_um(soma_completa_1_s1___vai_um));
  xor xor_3 (xor_3_out, y[1], carryIn);
  soma_completa soma_completa_2 (
    .vai_um(soma_completa_3_s1___vai_um), .x(x[1]), .y(xor_3_out), .s0(out_4[1]),
    .s1___vai_um(soma_completa_2_s1___vai_um));
  xor xor_4 (xor_4_out, y[0], carryIn);
  soma_completa soma_completa_3 (
    .vai_um(carryIn), .x(x[0]), .y(xor_4_out), .s0(out_4[0]), .s1___vai_um(soma_completa_3_s1___vai_um));

  // Notes on the sheet:
  //   saida
endmodule

module Exemplo0032 (
  input  in_1,
  input  [2:0] in_2,
  input  [2:0] in_3,
  output out_4,
  output _1___iguais
);

  wire [2:0] exemplo0031_1_out_4;

  Exemplo0031 exemplo0031_1 (.x(in_3), .y(in_2), .carryIn(in_1), .out_5(out_4), .out_4(exemplo0031_1_out_4));
  Comparador_igual comparador_igual_1 (.in_1(exemplo0031_1_out_4), .in_2(3'b000), .out_3(_1___iguais));

  // Notes on the sheet:
  //                        soma/subtracao
  //   0 - diferentes
endmodule
