// Logisim project Guia5.circ as structural Verilog
// FA
module soma (
  input  Vem_1,
  input  A,
  input  B,
  output S,
  output Sv1
);

  wire and_1_out, and_2_out, xor_1_out;

  xor xor_1 (xor_1_out, B, A);
  and and_1 (and_1_out, B, A);
  and and_2 (and_2_out, Vem_1, xor_1_out);
  or or_1 (Sv1, and_2_out, and_1_out);
  xor xor_2 (S, Vem_1, xor_1_out);

  // Notes on the sheet:
  //   s1
  //   s2
  //   s3
endmodule

module Exemplo0031 (
  input  [2:0] A,
  input  in_2,
  input  [2:0] B,
  output [2:0] out_4,
  output ov
);

  wire soma_1_sv1, soma_2_sv1, soma_3_sv1, xor_1_out, xor_2_out, xor_3_out;

  soma soma_1 (.Vem_1(in_2), .S(out_4[0]), .Sv1(soma_1_sv1), .A(A[0]), .B(xor_1_out));
  xor xor_1 (xor_1_out, B[0], in_2);
  soma soma_2 (.Vem_1(soma_1_sv1), .S(out_4[1]), .Sv1(soma_2_sv1), .A(xor_2_out), .B(A[1]));
  xor xor_2 (xor_2_out, B[1], in_2);
  soma soma_3 (.Vem_1(soma_2_sv1), .S(out_4[2]), .Sv1(soma_3_sv1), .A(xor_3_out), .B(A[2]));
  xor xor_3 (xor_3_out, B[2], in_2);
  xor xor_4 (ov, soma_3_sv1, in_2);

  // Notes on the sheet:
  //   s1
  //   s4
  //   s2
  //   s5
  //   s3
  //   s6
endmodule

module Exemplo0032 (
  input  [2:0] A,
  input  in_2,
  input  [2:0] B,
  output [2:0] out_4,
  output _2_falso,
  output Overfload
);

  wire soma_1_sv1, soma_2_sv1, soma_3_sv1, xor_1_out, xor_2_out, xor_3_out;

  soma soma_1 (.Vem_1(in_2), .S(out_4[0]), .Sv1(soma_1_sv1), .A(A[0]), .B(xor_1_out));
  xor xor_1 (xor_1_out, B[0], in_2);
  soma soma_2 (.Vem_1(soma_1_sv1), .S(out_4[1]), .Sv1(soma_2_sv1), .A(xor_2_out), .B(A[1]));
  xor xor_2 (xor_2_out, B[1], in_2);
  soma soma_3 (.Vem_1(soma_2_sv1), .S(out_4[2]), .Sv1(soma_3_sv1), .A(xor_3_out), .B(A[2]));
  xor xor_3 (xor_3_out, B[2], in_2);
  xor xor_4 (Overfload, soma_3_sv1, in_2);
  Zero zero_1 (.in_1(out_4), .out_3(_2_falso), .in_2(Overfload));

  // Notes on the sheet:
  //   Resultado Igual a Zero
  //   1 verdadeiro
endmodule

module Exemplo0033 (
  input  [2:0] A,
  input  _1___On,
  input  in_3,
  input  [2:0] B,
  output [2:0] out_5,
  output OverFload,
  output _2_falso,
  output Overfload_2
);

  wire soma_1_sv1, soma_2_sv1, soma_3_sv1, xor_1_out, xor_2_out, xor_3_out;
  wire [2:0] inc_1_1_out_4;

  inc_1 inc_1_1 (.in_1(A), .in_2(_1___On), .out_3(OverFload), .out_4(inc_1_1_out_4));
  soma soma_1 (.Vem_1(in_3), .S(out_5[0]), .Sv1(soma_1_sv1), .A(inc_1_1_out_4[0]), .B(xor_1_out));
  xor xor_1 (xor_1_out, B[0], in_3);
  soma soma_2 (.Vem_1(soma_1_sv1), .S(out_5[1]), .Sv1(soma_2_sv1), .A(xor_2_out), .B(inc_1_1_out_4[1]));
  xor xor_2 (xor_2_out, B[1], in_3);
  soma soma_3 (.Vem_1(soma_2_sv1), .S(out_5[2]), .Sv1(soma_3_sv1), .A(xor_3_out), .B(inc_1_1_out_4[2]));
  xor xor_3 (xor_3_out, B[2], in_3);
  xor xor_4 (Overfload_2, soma_3_sv1, in_3);
  Zero zero_1 (.in_1(out_5), .out_3(_2_falso), .in_2(Overfload_2));

  // Notes on the sheet:
  //   Inc 1
  //   0 - Off
  //   Inc 1
  //   Resultado Igual a Zero
  //   1 verdadeiro
endmodule

module Exemplo0034 (
  input  [2:0] A,
  input  _1___On,
  input  in_3,
  input  [2:0] B,
  output [2:0] out_5,
  output OverFload,
  output _2_falso,
  output Overfload_2,
  output OverFload_3,
  output Carry_in
);

  wire soma_1_sv1, soma_2_sv1, soma_3_sv1, xor_1_out, xor_2_out, xor_3_out;
  wire [2:0] inc_1_1_out_4;

  inc_1 inc_1_1 (.in_1(A), .in_2(_1___On), .out_3(OverFload), .out_4(inc_1_1_out_4));
  xor xor_1 (xor_1_out, B[0], in_3);
  xor xor_2 (xor_2_out, B[1], in_3);
  xor xor_3 (xor_3_out, B[2], in_3);
  soma soma_1 (.Vem_1(in_3), .S(out_5[0]), .Sv1(soma_1_sv1), .A(inc_1_1_out_4[0]), .B(xor_1_out));
  soma soma_2 (.Vem_1(soma_1_sv1), .S(out_5[1]), .Sv1(soma_2_sv1), .A(xor_2_out), .B(inc_1_1_out_4[1]));
  soma soma_3 (.Vem_1(soma_2_sv1), .S(out_5[2]), .Sv1(soma_3_sv1), .A(xor_3_out), .B(inc_1_1_out_4[2]));
  xor xor_4 (Overfload_2, soma_3_sv1, in_3);
  Zero zero_1 (.in_1(out_5), .out_3(_2_falso), .in_2(Overfload_2));

  assign Carry_in = in_3;
  assign OverFload_3 = Overfload_2;

  // Notes on the sheet:
  //   Inc 1
  //   0 - Off
  //   Inc 1
  //   Resultado Igual a Zero
  //   1 verdadeiro
endmodule

module Exemplo0035 (
  input  [2:0] A,
  input  Inc_1,
  input  in_3,
  input  [2:0] B,
  input  _0_Plus,
  input  On_Off,
  output OverFload,
  output [2:0] out_8,
  output _2_falso,
  output Overfload_2,
  output Overfload_MP,
  output OverFload_3,
  output Carry_in
);

  wire soma_1_sv1, soma_2_sv1, soma_3_sv1, xor_1_out, xor_2_out, xor_3_out;
  wire [2:0] inc_1_1_out_4, minus_plus_1_out_4;

  inc_1 inc_1_1 (.in_1(A), .in_2(Inc_1), .out_3(OverFload), .out_4(inc_1_1_out_4));
  Minus_plus minus_plus_1 (
    .in_3(inc_1_1_out_4), .out_4(minus_plus_1_out_4), .out_5(Overfload_MP), .minus_plus(_0_Plus),
    .on_Off(On_Off));
  xor xor_1 (xor_1_out, B[0], in_3);
  xor xor_2 (xor_2_out, B[1], in_3);
  xor xor_3 (xor_3_out, B[2], in_3);
  soma soma_1 (.Vem_1(in_3), .S(out_8[0]), .Sv1(soma_1_sv1), .A(minus_plus_1_out_4[0]), .B(xor_1_out));
  soma soma_2 (.Vem_1(soma_1_sv1), .S(out_8[1]), .Sv1(soma_2_sv1), .A(xor_2_out), .B(minus_plus_1_out_4[1]));
  soma soma_3 (.Vem_1(soma_2_sv1), .S(out_8[2]), .Sv1(soma_3_sv1), .A(xor_3_out), .B(minus_plus_1_out_4[2]));
  xor xor_4 (Overfload_2, soma_3_sv1, in_3);
  Zero zero_1 (.in_1(out_8), .out_3(_2_falso), .in_2(Overfload_2));

  assign Carry_in = in_3;
  assign OverFload_3 = Overfload_2;

  // Notes on the sheet:
  //   Inc 1
  //   1 minus
  //   0 - Off
  //   1 - On
  //   Resultado Igual a Zero
  //   1 verdadeiro
endmodule

module Exemplo0036 (
  input  [2:0] A,
  input  Inc_1,
  input  in_3,
  input  [2:0] B,
  input  Dec_1,
  input  _0_Plus,
  input  On_Off,
  output OverFload,
  output OverFload_2,
  output [2:0] out_10,
  output _2_falso,
  output Overfload_3,
  output Overfload_MP,
  output OverFload_4,
  output Carry_in
);

  wire soma_1_sv1, soma_2_sv1, soma_3_sv1, xor_1_out, xor_2_out, xor_3_out;
  wire [2:0] dec_1_1_out_4, inc_1_1_out_4, minus_plus_1_out_4;

  inc_1 inc_1_1 (.in_1(A), .in_2(Inc_1), .out_3(OverFload), .out_4(inc_1_1_out_4));
  Minus_plus minus_plus_1 (
    .in_3(inc_1_1_out_4), .out_4(minus_plus_1_out_4), .out_5(Overfload_MP), .minus_plus(_0_Plus),
    .on_Off(On_Off));
  Dec_1 dec_1_1 (.in_1(B), .in_2(Dec_1), .out_3(OverFload_2), .out_4(dec_1_1_out_4));
  xor xor_1 (xor_1_out, dec_1_1_out_4[0], in_3);
  xor xor_2 (xor_2_out, dec_1_1_out_4[1], in_3);
  xor xor_3 (xor_3_out, dec_1_1_out_4[2], in_3);
  soma soma_1 (.Vem_1(in_3), .S(out_10[0]), .Sv1(soma_1_sv1), .A(minus_plus_1_out_4[0]), .B(xor_1_out));
  soma soma_2 (.Vem_1(soma_1_sv1), .S(out_10[1]), .Sv1(soma_2_sv1), .A(xor_2_out), .B(minus_plus_1_out_4[1]));
  soma soma_3 (.Vem_1(soma_2_sv1), .S(out_10[2]), .Sv1(soma_3_sv1), .A(xor_3_out), .B(minus_plus_1_out_4[2]));
  xor xor_4 (Overfload_3, soma_3_sv1, in_3);
  Zero zero_1 (.in_1(out_10), .out_3(_2_falso), .in_2(Overfload_3));

  assign Carry_in = in_3;
  assign OverFload_4 = Overfload_3;

  // Notes on the sheet:
  //   Inc 1
  //   1 minus
  //   0 - Off
  //   1 - On
  //   0 - Off
  //   1 - On
  //   Dec 1
  //   Resultado Igual a Zero
  //   1 verdadeiro
endmodule

module Exemplo0037 (
  input  [2:0] A,
  input  _1___On,
  input  in_3,
  input  [2:0] B,
  output [1:0] _11_A_Maior,
  output [2:0] out_6,
  output OverFload,
  output _2_falso,
  output Overfload_2,
  output OverFload_3,
  output Carry_in
);

  wire soma_1_sv1, soma_2_sv1, soma_3_sv1, xor_1_out, xor_2_out, xor_3_out;
  wire [2:0] inc_1_1_out_4;

  inc_1 inc_1_1 (.in_1(A), .in_2(_1___On), .out_3(OverFload), .out_4(inc_1_1_out_4));
  Comparador comparador_1 (.A(inc_1_1_out_4), .B(B), .out_3(_11_A_Maior));
  xor xor_1 (xor_1_out, B[0], in_3);
  xor xor_2 (xor_2_out, B[1], in_3);
  xor xor_3 (xor_3_out, B[2], in_3);
  soma soma_1 (.Vem_1(in_3), .S(out_6[0]), .Sv1(soma_1_sv1), .A(inc_1_1_out_4[0]), .B(xor_1_out));
  soma soma_2 (.Vem_1(soma_1_sv1), .S(out_6[1]), .Sv1(soma_2_sv1), .A(xor_2_out), .B(inc_1_1_out_4[1]));
  soma soma_3 (.Vem_1(soma_2_sv1), .S(out_6[2]), .Sv1(soma_3_sv1), .A(xor_3_out), .B(inc_1_1_out_4[2]));
  xor xor_4 (Overfload_2, soma_3_sv1, in_3);
  Zero zero_1 (.in_1(out_6), .out_3(_2_falso), .in_2(Overfload_2));

  assign Carry_in = in_3;
  assign OverFload_3 = Overfload_2;

  // Notes on the sheet:
  //   Inc 1
  //   0 - Off
  //   Inc 1
  //   00 Igual
  //   01 B maior
  //   Resultado Igual a Zero
  //   1 verdadeiro
endmodule

// Z
module Zero (
  input  [2:0] in_1,
  input  in_2,
  output out_3
);

  wire xnor_1_out, xnor_2_out, xnor_3_out, xnor_4_out;

  xnor xnor_1 (xnor_1_out, in_2, 1'b0);
  xnor xnor_2 (xnor_2_out, in_1[0], 1'b0);
  xnor xnor_3 (xnor_3_out, in_1[1], 1'b0);
  xnor xnor_4 (xnor_4_out, in_1[2], 1'b0);
  and and_1 (out_3, xnor_2_out, xnor_1_out, xnor_4_out, xnor_3_out);
endmodule

// I 1
module inc_1 (
  input  [2:0] in_1,
  input  in_2,
  output out_3,
  output [2:0] out_4
);

  wire exemplo0031_1_ov;
  wire [2:0] and_1_out, and_2_out, exemplo0031_1_out_4, not_1_out;

  Exemplo0031 exemplo0031_1 (.out_4(exemplo0031_1_out_4), .ov(exemplo0031_1_ov), .A(in_1), .in_2(1'b0), .B(3'b001));
  assign not_1_out = ~{3{in_2}};  // NOT_Gate not_1, 3 bits wide
  assign and_1_out = exemplo0031_1_out_4 & {3{in_2}};  // AND_Gate and_1, 3 bits wide
  assign and_2_out = not_1_out & in_1;  // AND_Gate and_2, 3 bits wide
  and and_3 (out_3, exemplo0031_1_ov, in_2);
  assign out_4 = and_1_out | and_2_out;  // OR_Gate or_1, 3 bits wide
endmodule

// com
module Comparador (
  input  [2:0] A,
  input  [2:0] B,
  output [1:0] out_3
);

  wire and_1_out, and_2_out, and_3_out, and_4_out, exemplo0031_1_ov, exemplo0031_2_ov, not_1_out, xnor_1_out,
       xnor_2_out, xnor_3_out;

  Exemplo0031 exemplo0031_1 (.ov(exemplo0031_1_ov), .A(A), .in_2(1'b1), .B(B));  // open: out_4
  Exemplo0031 exemplo0031_2 (.ov(exemplo0031_2_ov), .A(B), .in_2(1'b1), .B(A));  // open: out_4
  xnor xnor_1 (xnor_1_out, B[0], A[0]);
  xnor xnor_2 (xnor_2_out, B[1], A[1]);
  xnor xnor_3 (xnor_3_out, B[2], A[2]);
  and and_1 (and_1_out, xnor_1_out, xnor_2_out, xnor_3_out);
  and and_2 (and_2_out, and_1_out, ~exemplo0031_1_ov, ~exemplo0031_2_ov);  // AND_Gate
  and and_3 (and_3_out, ~and_1_out, exemplo0031_1_ov, ~exemplo0031_2_ov);  // AND_Gate
  and and_4 (and_4_out, ~and_1_out, ~exemplo0031_1_ov, exemplo0031_2_ov);  // AND_Gate
  not not_1 (not_1_out, and_2_out);
  or or_1 (out_3[0], not_1_out, and_3_out);
  and and_5 (out_3[1], not_1_out, and_4_out);

  // Notes on the sheet:
  //   00 Igual
  //   01 B maior
  //   11 A Maior
endmodule

// MP
module Minus_plus (
  input  minus_plus,
  input  on_Off,
  input  [2:0] in_3,
  output [2:0] out_4,
  output out_5
);

  wire exemplo0031_1_ov;
  wire [2:0] and_1_out, and_2_out, exemplo0031_1_out_4;

  Exemplo0031 exemplo0031_1 (
    .out_4(exemplo0031_1_out_4), .ov(exemplo0031_1_ov), .A(in_3), .in_2(minus_plus), .B(3'b001));
  assign and_1_out = ~{3{on_Off}} & in_3;  // AND_Gate and_1, 3 bits wide
  assign and_2_out = {3{on_Off}} & exemplo0031_1_out_4;  // AND_Gate and_2, 3 bits wide
  and and_3 (out_5, exemplo0031_1_ov, on_Off);
  assign out_4 = and_1_out | and_2_out;  // OR_Gate or_1, 3 bits wide
endmodule

// D 1
module Dec_1 (
  input  [2:0] in_1,
  input  in_2,
  output out_3,
  output [2:0] out_4
);

  wire exemplo0031_1_ov;
  wire [2:0] and_1_out, and_2_out, exemplo0031_1_out_4, not_1_out;

  Exemplo0031 exemplo0031_1 (.out_4(exemplo0031_1_out_4), .ov(exemplo0031_1_ov), .A(in_1), .in_2(1'b1), .B(3'b001));
  assign not_1_out = ~{3{in_2}};  // NOT_Gate not_1, 3 bits wide
  assign and_1_out = exemplo0031_1_out_4 & {3{in_2}};  // AND_Gate and_1, 3 bits wide
  assign and_2_out = not_1_out & in_1;  // AND_Gate and_2, 3 bits wide
  and and_3 (out_3, exemplo0031_1_ov, in_2);
  assign out_4 = and_1_out | and_2_out;  // OR_Gate or_1, 3 bits wide
endmodule
