// Logisim project Projeto de circuito do Exemplo0031.circ as structural Verilog: 2 circuits, main circuit Exemplo0031
module Exemplo0031 (
  input  carryIn,
  input  a1,
  input  a0,
  input  b1,
  input  b0,
  output [2:0] out_6
);

  ALU_01 ALU_01 (.a1(a1), .a0(a0), .b1(b1), .b0(b0), .\Operação (carryIn), .s2(out_6[2]), .s1(out_6[1]), .s0(out_6[0]));

  // Notes on the sheet:
  //   Matrícula: 448662
  //   Nome: Josemar Alves Caetano
endmodule

module ALU_01 (
  input  \Operação ,
  input  a1,
  input  a0,
  input  b1,
  input  b0,
  output s2,
  output s1,
  output s0
);

  wire SC_1_carryout, xor1_out, xor2_out;

  xor xor1 (xor1_out, \Operação , b0);
  xor xor2 (xor2_out, \Operação , b1);
  Soma_Completa SC_1 (.a(a0), .b(xor1_out), .carryIn(\Operação ), .Soma(s0), .carryOut(SC_1_carryout));
  Soma_Completa SC_2 (.a(a1), .b(xor2_out), .carryIn(SC_1_carryout), .Soma(s1), .carryOut(s2));

  // Notes on the sheet:
  //   s1
  //   s0
  //   Matrícula: 448662
  //   Nome: Josemar Alves Caetano
endmodule
