// Logisim project Projeto de circuito do Exemplo0032.circ as structural Verilog: 3 circuits, main circuit Exemplo0032
module Exemplo0032 (
  input  carryIn,
  input  a1,
  input  a0,
  input  b1,
  input  b0,
  output [3:0] Flag_s
);

  ALU_02 ALU_02 (.a1(a1), .a0(a0), .b1(b1), .b0(b0), .carryIn(carryIn), .Flags(Flag_s));

  // Notes on the sheet:
  //   Z
  //   Z - Zero
  //   Matrícula: 448662
  //   Nome: Josemar Alves Caetano
endmodule

module ALU_02 (
  input  carryIn,
  input  a1,
  input  a0,
  input  b1,
  input  b0,
  output [3:0] Flags
);

  ALU_01 ALU_01 (.a1(a1), .a0(a0), .b1(b1), .b0(b0), .\Operação (carryIn), .s2(Flags[2]), .s1(Flags[1]), .s0(Flags[0]));
  Zero_Flag ZF (.a(Flags[2]), .b(Flags[1]), .c(Flags[0]), .Zero(Flags[3]));

  // Notes on the sheet:
  //   Z
  //   Z - Zero
endmodule

module Zero_Flag (
  input  a,
  input  b,
  input  c,
  output Zero
);

  wire OR_1_out;

  or OR_1 (OR_1_out, a, b, c);
  not not_1 (Zero, OR_1_out);
endmodule
