// Logisim project Projeto de circuito do Exemplo0034.circ as structural Verilog: 3 circuits, main circuit Exemplo0034
module Exemplo0034 (
  input  carryIn,
  input  a1,
  input  a0,
  input  b1,
  input  b0,
  output [4:0] Flags
);

  ALU_06 ALU_06 (.a1(a1), .a0(a0), .b1(b1), .b0(b0), .carryIn(carryIn), .Flags(Flags));

  // Notes on the sheet:
  //   O
  //   Z
  //   Z - Zero
  //   O - Overflow
  //   Matrícula: 448662
  //   Nome: Josemar Alves Caetano
endmodule

module ALU_06 (
  input  carryIn,
  input  a1,
  input  a0,
  input  b1,
  input  b0,
  output [4:0] Flags
);

  wire [2:0] ALU_01_out_6;

  Exemplo0031 ALU_01 (.a1(a1), .a0(a0), .b1(b1), .b0(b0), .carryIn(carryIn), .out_6(ALU_01_out_6));
  Decrementa DEC (.in_1(ALU_01_out_6), .Flags(Flags[3:0]));
  Zero_Flag ZF_1 (.a(Flags[0]), .b(Flags[1]), .c(Flags[2]), .Zero(Flags[4]));

  // Notes on the sheet:
  //   O
  //   Z
  //   Z - Zero
  //   O - Overflow
endmodule

module Decrementa (
  input  [2:0] in_1,
  output [3:0] Flags
);

  wire MS_1_vai_um, MS_2_soma, MS_2_vai_um, MS_3_vai_um, MS_4_soma, MS_4_vai_um, MS_5_soma, MS_5_vai_um,
       MS_6_vai_um;

  Meia_Soma MS_1 (.a(in_1[0]), .b(1'b1), .Vai_um(MS_1_vai_um), .Soma(Flags[0]));
  Meia_Soma MS_2 (.a(MS_1_vai_um), .b(in_1[1]), .Vai_um(MS_2_vai_um), .Soma(MS_2_soma));
  Meia_Soma MS_3 (.a(MS_2_soma), .b(1'b1), .Vai_um(MS_3_vai_um), .Soma(Flags[1]));
  Meia_Soma MS_4 (.a(MS_3_vai_um), .b(MS_2_vai_um), .Vai_um(MS_4_vai_um), .Soma(MS_4_soma));
  Meia_Soma MS_5 (.a(MS_4_soma), .b(in_1[2]), .Vai_um(MS_5_vai_um), .Soma(MS_5_soma));
  Meia_Soma MS_6 (.a(MS_5_soma), .b(1'b1), .Vai_um(MS_6_vai_um), .Soma(Flags[2]));
  or OR_1 (Flags[3], MS_4_vai_um, MS_5_vai_um, MS_6_vai_um);

  // Notes on the sheet:
  //   S
  //   O
  //   O - Overflow
endmodule
