// Logisim project Projeto de circuito do Exemplo0035.circ as structural Verilog: 2 circuits, main circuit Exemplo0035
module Exemplo0035 (
  input  a1,
  input  a0,
  input  b1,
  input  b0,
  output [2:0] out_5
);

  ALU_07 ALU_07 (.a1(a1), .a0(a0), .b1(b1), .b0(b0), .out_5(out_5));

  // Notes on the sheet:
  //   Matrícula: 448662
  //   Nome: Josemar Alves Caetano
endmodule

module ALU_07 (
  input  a1,
  input  a0,
  input  b1,
  input  b0,
  output [2:0] out_5
);

  wire AND_1_out, AND_2_out, AND_3_out, AND_5_out, AND_6_out, AND_7_out, not_1_out, not_2_out, not_3_out,
       not_4_out, OR_1_out, OR_3_out, XNOR_1_2_out, XNOR_1_out;

  not not_1 (not_1_out, a1);
  not not_2 (not_2_out, a0);
  not not_3 (not_3_out, b0);
  not not_4 (not_4_out, b1);
  and AND_5 (AND_5_out, a1, not_3_out);
  or OR_3 (OR_3_out, not_4_out, a0);
  and AND_7 (AND_7_out, a1, not_4_out);
  and AND_1 (AND_1_out, not_2_out, b0);
  or OR_1 (OR_1_out, not_1_out, b1);
  and AND_3 (AND_3_out, not_1_out, b1);
  xnor XNOR_1 (XNOR_1_out, a0, b0);
  xnor XNOR_1_2 (XNOR_1_2_out, a1, b1);
  and AND_2 (AND_2_out, AND_1_out, OR_1_out);
  and AND_4 (out_5[1], XNOR_1_out, XNOR_1_2_out);
  and AND_6 (AND_6_out, AND_5_out, OR_3_out);
  or OR_2 (out_5[0], AND_2_out, AND_3_out);
  or OR_4 (out_5[2], AND_6_out, AND_7_out);

  // Notes on the sheet:
  //   a1_n
  //   a0_n
  //   b0_n
  //   b1_n
  //   s0
  //   s1
  //   s3
  //   s4
  //   s5
  //   s6
  //   s7
  //   s9
  //   s2
  //   s8
endmodule
