// Logisim project Projeto de circuito do Exemplo0036.circ as structural Verilog: 3 circuits, main circuit Exemplo0036
module Exemplo0036 (
  input  carryIn,
  input  a1,
  input  a0,
  input  b1,
  input  b0,
  output [5:0] Flags
);

  ALU_04 ALU_04 (.a1(a1), .a0(a0), .b1(b1), .b0(b0), .carryIn(carryIn), .Flags(Flags));

  // Notes on the sheet:
  //   C
  //   O
  //   Z
  //   O - Overflow
  //   C - Carry
  //   Z - Zero
  //   Matrícula: 448662
  //   Nome: Josemar Alves Caetano
endmodule

module ALU_04 (
  input  carryIn,
  input  a1,
  input  a0,
  input  b1,
  input  b0,
  output [5:0] Flags
);

  ALU_01 ALU_01 (.a1(a1), .a0(a0), .b1(b1), .b0(b0), .\Operação (carryIn), .s2(Flags[2]), .s1(Flags[1]), .s0(Flags[0]));
  Zero_Flag ZF (.a(Flags[2]), .b(Flags[1]), .c(Flags[0]), .Zero(Flags[3]));
  Carry_e_Overflow CARRY_OVERFLOW (
    .a1(a1), .a0(a0), .b1(b1), .b0(b0), .carryIn(carryIn), .Carry(Flags[4]), .Overflow(Flags[5]));

  // Notes on the sheet:
  //   O
  //   C
  //   Z
  //   O - Overflow
  //   C - Carry
  //   Z - Zero
endmodule

module Carry_e_Overflow (
  input  carryIn,
  input  a1,
  input  a0,
  input  b1,
  input  b0,
  output Carry,
  output Overflow
);

  wire AND_1_out, AND_2_out, AND_3_out, AND_5_out, AND_6_out, AND_7_out, AND_8_out, not_1_out, not_2_out,
       not_3_out, OR_1_out, OR_2_out, XOR_1_out;

  not not_1 (not_1_out, b1);
  not not_2 (not_2_out, a0);
  and AND_1 (AND_1_out, a0, b1, b0);
  and AND_2 (AND_2_out, a1, a0, b0);
  and AND_3 (AND_3_out, a1, b1);
  and AND_5 (AND_5_out, a0, not_1_out, b0);
  and AND_6 (AND_6_out, a1, not_2_out);
  xor XOR_1 (XOR_1_out, b1, b0);
  and AND_7 (AND_7_out, a1, a0, b1);
  and AND_8 (AND_8_out, AND_6_out, XOR_1_out);
  not not_3 (not_3_out, carryIn);
  or OR_1 (OR_1_out, AND_1_out, AND_2_out, AND_3_out);
  and AND_4 (Carry, not_3_out, OR_1_out);
  or OR_2 (OR_2_out, AND_5_out, AND_8_out, AND_7_out);
  and AND_9 (Overflow, carryIn, OR_2_out);

  // Notes on the sheet:
  //   b1_n
  //   a0_n
  //   s0
  //   s1
  //   s2
  //   s4
  //   s5
  //   s6
  //   s7
  //   ci_n
  //   s3
  //   s8
  //   s9
endmodule
