// Logisim project Projeto de circuito do Exemplo0037.circ as structural Verilog: 3 circuits, main circuit Exemplo0037
module Exemplo0037 (
  input  carryIn,
  input  a1,
  input  a0,
  input  b1,
  input  b0,
  output [6:0] Flags
);

  ALU_05 ALU_05 (.a1(a1), .a0(a0), .b1(b1), .b0(b0), .carryIn(carryIn), .Flags(Flags));

  // Notes on the sheet:
  //   S
  //   C
  //   Z
  //   O
  //   C - Carry
  //   Z - Zero
  //   S - Sinal
  //   O - Overflow
  //   Matrícula: 448662
  //   Nome: Josemar Alves Caetano
endmodule

module ALU_05 (
  input  carryIn,
  input  a1,
  input  a0,
  input  b1,
  input  b0,
  output [6:0] Flags
);

  ALU_04 ALU_04 (.a1(a1), .a0(a0), .b1(b1), .b0(b0), .carryIn(carryIn), .Flags({Flags[6:4], Flags[2:0]}));
  Sinal SINAL (.a1(a1), .a0(a0), .b1(b1), .b0(b0), .carryIn(carryIn), .Sinal(Flags[3]));

  // Notes on the sheet:
  //   C
  //   S
  //   O
  //   Z
  //   O - Overflow
  //   C - Carry
  //   Z - Zero
  //   S - Sinal
endmodule

module Sinal (
  input  carryIn,
  input  a1,
  input  a0,
  input  b1,
  input  b0,
  output Sinal
);

  wire AND_1_out, AND_2_out, AND_3_out, not_1_out, not_2_out, OR_1_out;

  not not_1 (not_1_out, a1);
  not not_2 (not_2_out, a0);
  and AND_1 (AND_1_out, not_1_out, b1);
  and AND_2 (AND_2_out, not_1_out, not_2_out, b0);
  and AND_3 (AND_3_out, not_2_out, b1, b0);
  or OR_1 (OR_1_out, AND_1_out, AND_2_out, AND_3_out);
  and AND_4 (Sinal, carryIn, OR_1_out);

  // Notes on the sheet:
  //   a0_n
  //   a1_n
  //   s0
  //   s1
  //   s2
  //   s3
endmodule
