// Logisim project Soma completa.circ as structural Verilog: 2 circuits, main circuit Soma Completa
module Soma_Completa (
  input  a,
  input  b,
  input  carryIn,
  output Soma,
  output carryOut
);

  wire AND1_out, AND2_out, AND3_out, XOR1_out;

  xor XOR1 (XOR1_out, a, b);
  and AND1 (AND1_out, b, carryIn);
  and AND2 (AND2_out, a, b);
  and AND3 (AND3_out, a, carryIn);
  or OR1 (carryOut, AND1_out, AND2_out, AND3_out);
  xor XOR2 (Soma, XOR1_out, carryIn);

  // Notes on the sheet:
  //   s0
  //   s1
  //   s2
  //   s3
endmodule

module Meia_Soma (
  input  a,
  input  b,
  output Soma,
  output Vai_um
);

  and AND_1 (Vai_um, b, a);
  xor XOR_1 (Soma, a, b);
endmodule
