// Logisim project guia04Logisim.circ as structural Verilog: 10 circuits, main circuit main
module main (
);


  // Notes on the sheet:
  //   ARQUITETURA DE COMPUTADORES
  //   GUIA04
  //   ÁTILA MARTINS SILVA JÚNIOR - 449014
  //   30/08/2012
endmodule

module meia_soma (
  input  a,
  input  b,
  output s1,
  output s0
);

  and and_1 (s1, a, b);
  xor xor_1 (s0, a, b);

  // Notes on the sheet:
  //   MEIA SOMA
endmodule

// SC
module somador1bit (
  input  carry_in,
  input  a,
  input  in_3,
  output s1,
  output out_5
);

  wire meia_soma_1_s0, meia_soma_1_s1, meia_soma_2_s1;

  or or_1 (s1, meia_soma_1_s1, meia_soma_2_s1);
  meia_soma meia_soma_1 (.s1(meia_soma_1_s1), .a(a), .b(in_3), .s0(meia_soma_1_s0));
  meia_soma meia_soma_2 (.s1(meia_soma_2_s1), .a(carry_in), .b(meia_soma_1_s0), .s0(out_5));

  // Notes on the sheet:
  //   SOMADOR COMPLETO
  //   b
  //   s0
endmodule

// So3b
module exemplo0021 (
  input  [2:0] a,
  input  [2:0] b,
  input  carry_in,
  output carry_out,
  output [2:0] out_5
);

  wire somador1bit_2_s1, somador1bit_3_s1;

  somador1bit somador1bit_1 (.carry_in(a[2]), .a(b[2]), .in_3(somador1bit_2_s1), .s1(carry_out), .out_5(out_5[2]));
  somador1bit somador1bit_2 (
    .carry_in(a[1]), .a(b[1]), .in_3(somador1bit_3_s1), .s1(somador1bit_2_s1), .out_5(out_5[1]));
  somador1bit somador1bit_3 (.carry_in(a[0]), .a(b[0]), .in_3(carry_in), .s1(somador1bit_3_s1), .out_5(out_5[0]));

  // Notes on the sheet:
  //   Exemplo0021 - Átila Martins Silva Júnior - 449014
  //   SOMADOR COMPLETO / 3bits
  //   s
endmodule

// MD
module \meia_diferença  (
  input  a,
  input  b,
  output s1,
  output s0
);

  wire not_1_out;

  and and_1 (s1, not_1_out, b);
  not not_1 (not_1_out, a);
  xor xor_1 (s0, a, b);

  // Notes on the sheet:
  //   MEIA DIFERENÇA
endmodule

// SuC
module subtrator1bit (
  input  carry_in,
  input  a,
  input  b,
  output s,
  output carry_out
);

  wire \meia_diferença_1_s0 , \meia_diferença_1_s1 , \meia_diferença_2_s1 ;

  or or_1 (carry_out, \meia_diferença_2_s1 , \meia_diferença_1_s1 );
  \meia_diferença  \meia_diferença_1  (.s1(\meia_diferença_1_s1 ), .a(a), .b(b), .s0(\meia_diferença_1_s0 ));
  \meia_diferença  \meia_diferença_2  (.s1(\meia_diferença_2_s1 ), .a(carry_in), .b(\meia_diferença_1_s0 ), .s0(s));

  // Notes on the sheet:
  //   SUBTRATOR COMPLETO
endmodule

// Su3B
module exemplo0022 (
  input  [2:0] a,
  input  [2:0] b,
  input  carry_in,
  output carry_out,
  output [2:0] out_5
);

  wire subtrator1bit_2_carry_out, subtrator1bit_3_carry_out;

  subtrator1bit subtrator1bit_1 (
    .carry_in(a[2]), .a(b[2]), .b(subtrator1bit_2_carry_out), .carry_out(carry_out), .s(out_5[2]));
  subtrator1bit subtrator1bit_2 (
    .carry_in(a[1]), .a(b[1]), .b(subtrator1bit_3_carry_out), .carry_out(subtrator1bit_2_carry_out),
    .s(out_5[1]));
  subtrator1bit subtrator1bit_3 (
    .carry_in(a[0]), .a(b[0]), .b(carry_in), .carry_out(subtrator1bit_3_carry_out), .s(out_5[0]));

  // Notes on the sheet:
  //   SUBTRATOR/ 3bits
  //   Exemplo0022 - Átila Martins Silva Júnior - 449014
  //   s
endmodule

module exemplo0023 (
  input  [2:0] a,
  input  [2:0] b,
  output out_3
);

  wire xor_1_out, xor_2_out, xor_3_out;

  xor xor_1 (xor_1_out, a[2], b[2]);
  xor xor_2 (xor_2_out, a[1], b[1]);
  nor nor_1 (out_3, xor_1_out, xor_2_out, xor_3_out);
  xor xor_3 (xor_3_out, a[0], b[0]);

  // Notes on the sheet:
  //   COMPARADOR DE IGUALDADE / 3bits
  //   Exemplo0023 - Átila Martins Silva Júnior - 449014
  //   s0
endmodule

module exemplo0024 (
  input  [2:0] a,
  input  [2:0] b,
  output s0
);

  wire xor_1_out, xor_2_out, xor_3_out;

  xor xor_1 (xor_1_out, a[2], b[2]);
  xor xor_2 (xor_2_out, a[1], b[1]);
  or or_1 (s0, xor_1_out, xor_2_out, xor_3_out);
  xor xor_3 (xor_3_out, a[0], b[0]);

  // Notes on the sheet:
  //   Exemplo0025 - Átila Martins Silva Júnior - 449014
  //   COMPARADOR DE DIFERENÇA / 3bits
endmodule

module exemplo0025 (
  input  [2:0] a,
  input  in_2,
  input  [2:0] in_3,
  output [2:0] s0
);

  wire [2:0] not_1_out;

  assign not_1_out = ~a;  // NOT_Gate not_1, 3 bits wide
  exemplo0021 exemplo0021_1 (.a(in_3), .b(not_1_out), .carry_in(in_2), .out_5(s0));  // open: carry_out

  // Notes on the sheet:
  //   COMPLEMENTO DE 2 / 3bitis 
  //   Exemplo0025 - Átila Martins Silva Júnior - 449014
  //   # 000 para complemento de 2
  //   1-Para compelemntar de 2
  //   0-Para complementar de 1
endmodule
