// Logisim project circ.circ as structural Verilog
module FullAdder (
  input  in_1,
  input  in_2,
  input  in_3,
  output out_4,
  output out_5
);

  wire and_1_out, and_2_out, xor_1_out;

  xor xor_1 (xor_1_out, in_1, in_2);
  xor xor_2 (out_4, xor_1_out, in_3);
  and and_1 (and_1_out, in_3, xor_1_out);
  and and_2 (and_2_out, in_2, in_1, in_1);
  or or_1 (out_5, and_1_out, and_2_out);
endmodule

module Exemplo0031 (
  input  [2:0] in_1,
  input  [2:0] in_2,
  input  in_3,
  output out_4,
  output [2:0] out_5
);

  wire fulladder_1_out_5, fulladder_2_out_5, fulladder_3_out_5;
  wire [2:0] xor_1_out;

  assign xor_1_out = in_2 ^ {3{in_3}};  // XOR_Gate xor_1, 3 bits wide
  FullAdder fulladder_1 (.in_1(in_1[0]), .in_2(xor_1_out[0]), .in_3(in_3), .out_4(out_5[0]), .out_5(fulladder_1_out_5));
  FullAdder fulladder_2 (
    .in_1(in_1[1]), .in_2(xor_1_out[1]), .in_3(fulladder_1_out_5), .out_4(out_5[1]), .out_5(fulladder_2_out_5));
  FullAdder fulladder_3 (
    .in_1(in_1[2]), .in_2(xor_1_out[2]), .in_3(fulladder_2_out_5), .out_4(out_5[2]), .out_5(fulladder_3_out_5));
  xor xor_2 (out_4, fulladder_3_out_5, in_3);
endmodule

module Exemplo0032 (
  input  [2:0] in_1,
  input  [2:0] in_2,
  input  in_3,
  output out_4,
  output [2:0] out_5,
  output Flag0
);

  wire fulladder_1_out_5, fulladder_2_out_5, fulladder_3_out_5;
  wire [2:0] xor_1_out;

  assign xor_1_out = in_2 ^ {3{in_3}};  // XOR_Gate xor_1, 3 bits wide
  FullAdder fulladder_1 (.in_1(in_1[0]), .in_2(xor_1_out[0]), .in_3(in_3), .out_4(out_5[0]), .out_5(fulladder_1_out_5));
  flag0 flag0_1 (.in_1(out_5), .out_2(Flag0));
  FullAdder fulladder_2 (
    .in_1(in_1[1]), .in_2(xor_1_out[1]), .in_3(fulladder_1_out_5), .out_4(out_5[1]), .out_5(fulladder_2_out_5));
  FullAdder fulladder_3 (
    .in_1(in_1[2]), .in_2(xor_1_out[2]), .in_3(fulladder_2_out_5), .out_4(out_5[2]), .out_5(fulladder_3_out_5));
  xor xor_2 (out_4, fulladder_3_out_5, in_3);
endmodule

module flag0 (
  input  [2:0] in_1,
  output out_2
);

  wire not_1_out, not_2_out, not_3_out;

  not not_1 (not_1_out, in_1[0]);
  not not_2 (not_2_out, in_1[1]);
  not not_3 (not_3_out, in_1[2]);
  and and_1 (out_2, not_1_out, not_2_out, not_3_out);
endmodule
