// Logisim project Detecção de Carry & OverFlow.circ as structural Verilog: 3 circuits, main circuit main
module main (
  input  [2:0] a,
  input  [2:0] b,
  input  op,
  output overFlow,
  output Carry_out,
  output [1:0] s,
  output Zero_flag
);

  wire f_a_1_carryout, f_a_2_carryout, f_a_3_carryout, xor_2_out, xor_3_out, xor_4_out;

  xor xor_1 (overFlow, op, f_a_1_carryout);
  nor nor_1 (Zero_flag, overFlow, s[0], Carry_out, s[1]);
  xor xor_2 (xor_2_out, b[2], op);
  F_A f_a_1 (.carryOut(f_a_1_carryout), .a(a[2]), .b(xor_2_out), .s(Carry_out), .carry_In(f_a_2_carryout));
  xor xor_3 (xor_3_out, b[1], op);
  F_A f_a_2 (.carryOut(f_a_2_carryout), .a(a[1]), .b(xor_3_out), .s(s[1]), .carry_In(f_a_3_carryout));
  xor xor_4 (xor_4_out, b[0], op);
  F_A f_a_3 (.carryOut(f_a_3_carryout), .a(a[0]), .b(xor_4_out), .s(s[0]), .carry_In(op));
endmodule

module H_A (
  input  a,
  input  b,
  output s1,
  output s0
);

  and and_1 (s1, b, a);
  xor xor_1 (s0, a, b);
endmodule

module F_A (
  input  a,
  input  b,
  input  carry_In,
  output carryOut,
  output s
);

  wire h_a_1_s0, h_a_1_s1, h_a_2_s1;

  or or_1 (carryOut, h_a_1_s1, h_a_2_s1);
  H_A h_a_1 (.a(a), .b(b), .s1(h_a_1_s1), .s0(h_a_1_s0));
  H_A h_a_2 (.a(h_a_1_s0), .b(carry_In), .s1(h_a_2_s1), .s0(s));
endmodule
