// Logisim project Incremento de 1.circ as structural Verilog: 3 circuits, main circuit main
module main (
  input  [2:0] in_1,
  output [3:0] out_2
);

  wire f_a_1_carryout, f_a_2_carryout, f_a_3_carryout;

  xor xor_1 (out_2[3], f_a_1_carryout, 1'b0);
  F_A f_a_1 (.carryOut(f_a_1_carryout), .a(in_1[2]), .b(1'b0), .s(out_2[2]), .carry_In(f_a_2_carryout));
  F_A f_a_2 (.carryOut(f_a_2_carryout), .a(in_1[1]), .b(1'b0), .s(out_2[1]), .carry_In(f_a_3_carryout));
  F_A f_a_3 (.carryOut(f_a_3_carryout), .a(in_1[0]), .b(1'b1), .s(out_2[0]), .carry_In(1'b0));
endmodule

module H_A (
  input  a,
  input  b,
  output s1,
  output s0
);

  and and_1 (s1, b, a);
  xor xor_1 (s0, a, b);
endmodule

module F_A (
  input  a,
  input  b,
  input  carry_In,
  output carryOut,
  output s
);

  wire h_a_1_s0, h_a_1_s1, h_a_2_s1;

  or or_1 (carryOut, h_a_1_s1, h_a_2_s1);
  H_A h_a_1 (.a(a), .b(b), .s1(h_a_1_s1), .s0(h_a_1_s0));
  H_A h_a_2 (.a(h_a_1_s0), .b(carry_In), .s1(h_a_2_s1), .s0(s));
endmodule
