// Logisim project Circuitos.circ as structural Verilog: 8 circuits, main circuit main
module main (
  input  a,
  input  b,
  output Carry_in,
  output S
);

  and and_1 (Carry_in, a, b);
  xor xor_1 (S, a, b);

  // Notes on the sheet:
  //   Arquitetura de Computadores - Guia 5
  //   Aluno: Isabel Bicalho Amaro
  //   Matricula: 451580
endmodule

// FA
module Full_Adder (
  input  a,
  input  b,
  input  First_Carry,
  output Next_Carry,
  output S
);

  wire and1_out, and2_out, xor1_out;

  and and1 (and1_out, a, b);
  or or1 (Next_Carry, and1_out, and2_out);
  and and2 (and2_out, First_Carry, xor1_out);
  xor xor1 (xor1_out, a, b);
  xor xor2 (S, xor1_out, First_Carry);

  // Notes on the sheet:
  //   s3
  //   s3
  //   Next Carry
  //   First Carry
  //   s1
  //   s2
  //   s2
  //   s1
  //   s1
  //   First Carry
endmodule

module Questao_1 (
  input  [2:0] x,
  input  [2:0] y,
  input  Chave___First_Carry,
  output Carry_Out,
  output [2:0] S
);

  wire full_adder_1_next_carry, full_adder_2_next_carry, full_adder_3_next_carry, xor1_out, xor2_out,
       xor3_out;

  xor xor4 (Carry_Out, Chave___First_Carry, full_adder_1_next_carry);
  xor xor3 (xor3_out, y[2], Chave___First_Carry);
  Full_Adder full_adder_1 (
    .Next_Carry(full_adder_1_next_carry), .a(x[2]), .b(xor3_out), .S(S[2]),
    .First_Carry(full_adder_2_next_carry));
  xor xor1 (xor1_out, y[0], Chave___First_Carry);
  xor xor2 (xor2_out, y[1], Chave___First_Carry);
  Full_Adder full_adder_2 (
    .Next_Carry(full_adder_2_next_carry), .a(x[1]), .b(xor2_out), .S(S[1]),
    .First_Carry(full_adder_3_next_carry));
  Full_Adder full_adder_3 (
    .Next_Carry(full_adder_3_next_carry), .a(x[0]), .b(xor1_out), .S(S[0]), .First_Carry(Chave___First_Carry));

  // Notes on the sheet:
  //   c
  //   c3
  //   y2
  //   c
  //   y1
  //   s2
  //   x1
  //   x2
  //   c2
  //   y0
  //   c
  //   c
  //   s1
  //   s0
  //   x0
  //   c1
  //   c
  //   Soma - 0
  //   Subtração - 1
endmodule

module Questao_2 (
  input  [2:0] x,
  input  [2:0] y,
  input  Chave___First_Carry,
  output Carry_Out,
  output ZERO_flag,
  output [2:0] S
);

  wire full_adder_1_next_carry, full_adder_2_next_carry, full_adder_3_next_carry, xor1_out, xor2_out,
       xor3_out;

  xor xor4 (Carry_Out, Chave___First_Carry, full_adder_1_next_carry);
  xor xor3 (xor3_out, y[2], Chave___First_Carry);
  Full_Adder full_adder_1 (
    .Next_Carry(full_adder_1_next_carry), .a(x[2]), .b(xor3_out), .S(S[2]),
    .First_Carry(full_adder_3_next_carry));
  xor xor2 (xor2_out, y[1], Chave___First_Carry);
  xor xor1 (xor1_out, y[0], Chave___First_Carry);
  Full_Adder full_adder_2 (
    .Next_Carry(full_adder_2_next_carry), .a(x[0]), .b(xor1_out), .S(S[0]), .First_Carry(Chave___First_Carry));
  Full_Adder full_adder_3 (
    .Next_Carry(full_adder_3_next_carry), .a(x[1]), .b(xor2_out), .S(S[1]),
    .First_Carry(full_adder_2_next_carry));
  nor nor1 (ZERO_flag, S[2], S[1], S[0]);

  // Notes on the sheet:
  //   c
  //   c3
  //   y2
  //   c
  //   y1
  //   s2
  //   x2
  //   x1
  //   c2
  //   c
  //   y0
  //   c
  //   s1
  //   s0
  //   x0
  //   c1
  //   c
  //   1 - Resultado 0
  //   0 - Resultado nao é zero
  //   Soma - 0
  //   Subtração - 1
endmodule

module Questao_3 (
  input  [2:0] x,
  input  [2:0] y,
  input  Chave___First_Carry,
  output Carry_Out,
  output ZERO_flag,
  output [2:0] S
);

  wire full_adder_1_next_carry, full_adder_2_next_carry, full_adder_3_next_carry, incremento_de_1_1__0,
       incremento_de_1_1__1, incremento_de_1_1__2, xor1_out, xor2_out, xor3_out;

  xor xor4 (Carry_Out, Chave___First_Carry, full_adder_1_next_carry);
  Incremento_de_1 incremento_de_1_1 (
    .b2(x[2]), .b1(x[1]), .b0(x[0]), ._2(incremento_de_1_1__2), ._1(incremento_de_1_1__1),
    ._0(incremento_de_1_1__0));
  xor xor2 (xor2_out, y[1], Chave___First_Carry);
  xor xor3 (xor3_out, y[2], Chave___First_Carry);
  Full_Adder full_adder_1 (
    .Next_Carry(full_adder_1_next_carry), .a(incremento_de_1_1__2), .b(xor3_out), .S(S[2]),
    .First_Carry(full_adder_2_next_carry));
  Full_Adder full_adder_2 (
    .Next_Carry(full_adder_2_next_carry), .a(incremento_de_1_1__1), .b(xor2_out), .S(S[1]),
    .First_Carry(full_adder_3_next_carry));
  xor xor1 (xor1_out, y[0], Chave___First_Carry);
  Full_Adder full_adder_3 (
    .Next_Carry(full_adder_3_next_carry), .a(incremento_de_1_1__0), .b(xor1_out), .S(S[0]),
    .First_Carry(Chave___First_Carry));
  nor nor1 (ZERO_flag, S[2], S[1], S[0]);

  // Notes on the sheet:
  //   c
  //   x2
  //   c3
  //   y2
  //   c
  //   y1
  //   c
  //   s1
  //   s2
  //   x1
  //   x0
  //   c1
  //   c2
  //   c
  //   y0
  //   s0
  //   c
  //   1 - Resultado 0
  //   0 - Resultado nao é zero
  //   Soma - 0
  //   Subtração - 1
endmodule

module Questao_4 (
  input  [2:0] x,
  input  [2:0] y,
  input  Chave___First_Carry,
  output ZERO_flag,
  output Carry_Out,
  output [2:0] S,
  output Overflow
);

  wire full_adder_1_next_carry, full_adder_2_next_carry, full_adder_3_next_carry, xor1_out, xor2_out,
       xor3_out, xor5_out;

  xor xor4 (Carry_Out, Chave___First_Carry, full_adder_1_next_carry);
  xor xor5 (xor5_out, full_adder_1_next_carry, full_adder_2_next_carry);
  or or1 (Overflow, Carry_Out, xor5_out);
  xor xor3 (xor3_out, y[2], Chave___First_Carry);
  Full_Adder full_adder_1 (
    .Next_Carry(full_adder_1_next_carry), .a(x[2]), .b(xor3_out), .S(S[2]),
    .First_Carry(full_adder_2_next_carry));
  xor xor2 (xor2_out, y[1], Chave___First_Carry);
  xor xor1 (xor1_out, y[0], Chave___First_Carry);
  Full_Adder full_adder_2 (
    .Next_Carry(full_adder_2_next_carry), .a(x[1]), .b(xor2_out), .S(S[1]),
    .First_Carry(full_adder_3_next_carry));
  Full_Adder full_adder_3 (
    .Next_Carry(full_adder_3_next_carry), .a(x[0]), .b(xor1_out), .S(S[0]), .First_Carry(Chave___First_Carry));
  nor nor1 (ZERO_flag, S[2], S[1], S[0]);

  // Notes on the sheet:
  //   1 - Resultado 0
  //   0 - Resultado nao é zero
  //   Soma - 0
  //   Subtração - 1
endmodule

module Questao_5 (
  input  [2:0] x,
  input  [2:0] y,
  input  Chave___First_Carry,
  output ZERO_flag,
  output Carry_Out,
  output [2:0] S,
  output Overflow,
  output Sinal
);

  wire full_adder_1_next_carry, full_adder_2_next_carry, full_adder_3_next_carry, xor1_out, xor2_out,
       xor3_out, xor5_out;

  xor xor4 (Carry_Out, Chave___First_Carry, full_adder_1_next_carry);
  or or1 (Overflow, Carry_Out, xor5_out);
  xor xor3 (xor3_out, y[2], Chave___First_Carry);
  Full_Adder full_adder_1 (
    .Next_Carry(full_adder_1_next_carry), .a(x[2]), .b(xor3_out), .S(S[2]),
    .First_Carry(full_adder_2_next_carry));
  xor xor5 (xor5_out, full_adder_1_next_carry, full_adder_2_next_carry);
  xor xor1 (xor1_out, y[0], Chave___First_Carry);
  xor xor2 (xor2_out, y[1], Chave___First_Carry);
  Full_Adder full_adder_2 (
    .Next_Carry(full_adder_2_next_carry), .a(x[1]), .b(xor2_out), .S(S[1]),
    .First_Carry(full_adder_3_next_carry));
  Full_Adder full_adder_3 (
    .Next_Carry(full_adder_3_next_carry), .a(x[0]), .b(xor1_out), .S(S[0]), .First_Carry(Chave___First_Carry));
  nor nor1 (ZERO_flag, S[2], S[1], S[0]);

  assign Sinal = S[2];

  // Notes on the sheet:
  //   1 - Resultado 0
  //   0 - Resultado nao é zero
  //   Soma - 0
  //   Subtração - 1
endmodule

// inc
module Incremento_de_1 (
  input  b2,
  input  b1,
  input  b0,
  output _2,
  output _1,
  output _0
);

  wire full_adder_1_next_carry, full_adder_3_next_carry;

  Full_Adder full_adder_1 (
    .Next_Carry(full_adder_1_next_carry), .a(b1), .b(b0), .S(_1), .First_Carry(full_adder_3_next_carry));
  Full_Adder full_adder_2 (.a(b2), .b(b0), .S(_2), .First_Carry(full_adder_1_next_carry));  // open: Next_Carry
  Full_Adder full_adder_3 (.Next_Carry(full_adder_3_next_carry), .a(b0), .b(1'b1), .S(_0), .First_Carry(b0));
  // also tied to GND on the sheet: b0
endmodule
