// Logisim project Exemplo0033.circ as structural Verilog: 3 circuits, main circuit main
module main (
  input  [2:0] a,
  output [3:0] s
);

  wire fulladder_1_carryout, fulladder_2_carryout, fulladder_3_carryout;

  xor xor_1 (s[3], fulladder_1_carryout, 1'b0);
  fullAdder fulladder_1 (
    .carryOut(fulladder_1_carryout), .a(a[2]), .b(1'b0), .s(s[2]), .carry_In(fulladder_2_carryout));
  fullAdder fulladder_2 (
    .carryOut(fulladder_2_carryout), .a(a[1]), .b(1'b0), .s(s[1]), .carry_In(fulladder_3_carryout));
  fullAdder fulladder_3 (.carryOut(fulladder_3_carryout), .a(a[0]), .b(1'b1), .s(s[0]), .carry_In(1'b0));

  // Notes on the sheet:
  //   Pedro Henrique Lima Pinheiro
  //   451605
endmodule

// H.A.
module halfAdder (
  input  a,
  input  b,
  output s1,
  output s0
);

  and and_1 (s1, b, a);
  xor xor_1 (s0, a, b);

  // Notes on the sheet:
  //   Pedro Henrique Lima Pinheiro
  //   451605
endmodule

// F.A.
module fullAdder (
  input  a,
  input  b,
  input  carry_In,
  output carryOut,
  output s
);

  wire halfadder_1_s0, halfadder_1_s1, halfadder_2_s1;

  halfAdder halfadder_1 (.a(a), .b(b), .s1(halfadder_1_s1), .s0(halfadder_1_s0));
  or or_1 (carryOut, halfadder_1_s1, halfadder_2_s1);
  halfAdder halfadder_2 (.a(halfadder_1_s0), .b(carry_In), .s1(halfadder_2_s1), .s0(s));

  // Notes on the sheet:
  //   Pedro Henrique Lima Pinheiro
  //   451605
endmodule
