// Logisim project Exemplo0034.circ as structural Verilog: 3 circuits, main circuit main
module main (
  input  [2:0] a,
  input  [2:0] b,
  input  op,
  output overFlow,
  output carry_out,
  output [1:0] s,
  output ZERO_flag
);

  wire fulladder_1_carryout, fulladder_2_carryout, fulladder_3_carryout, xor_2_out, xor_3_out, xor_4_out;

  nor nor_1 (ZERO_flag, s[0], s[1], carry_out, overFlow);
  // Probe on a
  xor xor_1 (overFlow, op, fulladder_1_carryout);
  xor xor_2 (xor_2_out, b[1], op);
  xor xor_3 (xor_3_out, b[2], op);
  fullAdder fulladder_1 (
    .carryOut(fulladder_1_carryout), .a(a[2]), .b(xor_3_out), .s(carry_out), .carry_In(fulladder_2_carryout));
  // Probe on b
  xor xor_4 (xor_4_out, b[0], op);
  fullAdder fulladder_2 (
    .carryOut(fulladder_2_carryout), .a(a[1]), .b(xor_2_out), .s(s[1]), .carry_In(fulladder_3_carryout));
  fullAdder fulladder_3 (.carryOut(fulladder_3_carryout), .a(a[0]), .b(xor_4_out), .s(s[0]), .carry_In(op));

  // Notes on the sheet:
  //   Pedro Henrique Lima Pinheiro
  //   451605
endmodule

// H.A.
module halfAdder (
  input  a,
  input  b,
  output s1,
  output s0
);

  and and_1 (s1, b, a);
  xor xor_1 (s0, a, b);

  // Notes on the sheet:
  //   Pedro Henrique Lima Pinheiro
  //   451605
endmodule

// F.A.
module fullAdder (
  input  a,
  input  b,
  input  carry_In,
  output carryOut,
  output s
);

  wire halfadder_1_s0, halfadder_1_s1, halfadder_2_s1;

  halfAdder halfadder_1 (.a(a), .b(b), .s1(halfadder_1_s1), .s0(halfadder_1_s0));
  or or_1 (carryOut, halfadder_1_s1, halfadder_2_s1);
  halfAdder halfadder_2 (.a(halfadder_1_s0), .b(carry_In), .s1(halfadder_2_s1), .s0(s));

  // Notes on the sheet:
  //   Pedro Henrique Lima Pinheiro
  //   451605
endmodule
