// Logisim project Exemplo0033.circ as structural Verilog: 3 circuits, main circuit main
// H.A.
module halfAdder (
  input  a,
  input  b,
  output out_3,
  output out_4
);

  and and_1 (out_3, a, b);
  xor xor_1 (out_4, a, b);
endmodule

// F.A.
module fullAdder (
  input  a,
  input  b,
  input  carry_In,
  output carryOut,
  output s
);

  wire halfadder_1_out_3, halfadder_1_out_4, halfadder_2_out_3;

  or or_1 (carryOut, halfadder_1_out_3, halfadder_2_out_3);
  halfAdder halfadder_1 (.a(a), .b(b), .out_3(halfadder_1_out_3), .out_4(halfadder_1_out_4));
  halfAdder halfadder_2 (.a(halfadder_1_out_4), .b(carry_In), .out_3(halfadder_2_out_3), .out_4(s));
endmodule

module main (
  input  [3:0] a,
  output overFlow,
  output [3:0] out_3
);

  wire fulladder_1_carryout, fulladder_3_carryout, fulladder_4_carryout;

  // Probe on a
  fullAdder fulladder_1 (
    .carryOut(fulladder_1_carryout), .a(a[2]), .b(1'b0), .s(out_3[2]), .carry_In(fulladder_4_carryout));
  fullAdder fulladder_2 (.carryOut(overFlow), .a(a[3]), .b(1'b0), .s(out_3[3]), .carry_In(fulladder_1_carryout));
  // Probe on out_3
  fullAdder fulladder_3 (.carryOut(fulladder_3_carryout), .a(a[0]), .b(1'b1), .s(out_3[0]), .carry_In(1'b0));
  fullAdder fulladder_4 (
    .carryOut(fulladder_4_carryout), .a(a[1]), .b(1'b0), .s(out_3[1]), .carry_In(fulladder_3_carryout));
endmodule
