// Logisim project Exemplo0037.circ as structural Verilog: 1 circuit, main circuit main
module main (
  input  in_1,
  input  X2,
  input  X1,
  input  X0,
  input  Y0,
  input  Y2,
  input  Y1,
  output out_8,
  output out_9,
  output out_10,
  output out_11,
  output out_12,
  output carry,
  output overflow,
  output Negativo___1
);

  wire and_1_out, and_2_out, and_3_out, and_4_out, and_5_out, and_6_out, or_1_out, or_2_out, or_3_out,
       xor_1_out, xor_2_out, xor_3_out, xor_4_out, xor_5_out, xor_6_out;

  xor xor_1 (xor_1_out, Y0, in_1);
  xor xor_2 (xor_2_out, Y1, in_1);
  xor xor_3 (xor_3_out, Y2, in_1);
  xor xor_4 (xor_4_out, X0, xor_1_out);
  xor xor_5 (xor_5_out, X1, xor_2_out);
  xor xor_6 (xor_6_out, X2, xor_3_out);
  xor xor_7 (out_11, xor_4_out, in_1);
  and and_1 (and_1_out, in_1, xor_4_out);
  and and_2 (and_2_out, X0, xor_1_out);
  xor xor_8 (out_10, xor_5_out, or_1_out);
  and and_3 (and_3_out, or_1_out, xor_5_out);
  and and_4 (and_4_out, X1, xor_2_out);
  xor xor_9 (out_9, xor_6_out, or_2_out);
  and and_5 (and_5_out, or_2_out, xor_6_out);
  and and_6 (and_6_out, X2, xor_3_out);
  or or_1 (or_1_out, and_1_out, and_2_out);
  or or_2 (or_2_out, and_3_out, and_4_out);
  or or_3 (or_3_out, and_5_out, and_6_out);
  nor nor_1 (out_12, out_8, out_11, out_10, out_9);
  xor xor_10 (carry, in_1, or_3_out);
  xor xor_11 (overflow, out_8, out_9);
  and and_7 (Negativo___1, out_8, in_1);
  xor xor_12 (out_8, in_1, or_3_out);

  // Notes on the sheet:
  //   Rodolfo Herman - 451612
  //   Igual a zero = 1
  //   Nao é igual a zero = 0
  //   Positivo = 0
endmodule
