// Logisim project Exemplo0032.circ as structural Verilog: 2 circuits, main circuit main
module main (
  input  in_1,
  input  in_2,
  input  in_3,
  output out_4,
  output out_5,
  output zero_flag
);

  wire som_1_out_5, xor_2_out;

  xor xor_1 (out_4, in_3, som_1_out_5);
  xor xor_2 (xor_2_out, in_2, in_3);
  Som som_1 (.in_1(in_3), .in_2(xor_2_out), .in_3(in_1), .out_5(som_1_out_5), .out_4(out_5));
  nor nor_1 (zero_flag, out_4, out_5);

  // Notes on the sheet:
  //   Nome: Tiago Matta Machado Zaidan
  //   Matricula: 451620
  //   Exemplo0032
endmodule

module Som (
  input  in_1,
  input  in_2,
  input  in_3,
  output out_4,
  output out_5
);

  wire and_1_out, and_2_out, xor_1_out;

  xor xor_1 (xor_1_out, in_2, in_3);
  and and_1 (and_1_out, in_3, in_2);
  xor xor_2 (out_4, in_1, xor_1_out);
  and and_2 (and_2_out, in_1, xor_1_out);
  xor xor_3 (out_5, and_2_out, and_1_out);
endmodule
