// Logisim project Exemplo0034.circ as structural Verilog: 4 circuits, main circuit main
module main (
  input  in_1,
  input  in_2,
  input  in_3,
  output out_4,
  output out_5,
  output overFlow,
  output out_7,
  output out_8,
  output out_9,
  output out_10,
  output zero_flag,
  output sinal
);

  wire som_1_out_5, xor_2_out;

  xor xor_1 (out_4, in_3, som_1_out_5);
  xor xor_2 (xor_2_out, in_2, in_3);
  som som_1 (.in_1(in_3), .in_2(xor_2_out), .in_3(in_1), .out_5(som_1_out_5), .out_4(out_5));
  nor nor_1 (zero_flag, out_4, out_5);
  inc inc_1 (.in_1(in_1), .out_2(out_8), .out_3(out_7));
  and and_1 (sinal, out_4, in_3);
  dec dec_1 (.in_1(in_1), .out_2(out_10), .out_3(out_9));

  assign overFlow = out_4;

  // Notes on the sheet:
  //   Nome: Tiago Matta Machado Zaidan
  //   Matricula: 451620
  //   Exemplo0034
  //   o sinal e negativo apenas nas subtracoes
endmodule

module som (
  input  in_1,
  input  in_2,
  input  in_3,
  output out_4,
  output out_5
);

  wire and_1_out, and_2_out, xor_1_out;

  xor xor_1 (xor_1_out, in_2, in_3);
  and and_1 (and_1_out, in_3, in_2);
  xor xor_2 (out_4, in_1, xor_1_out);
  and and_2 (and_2_out, in_1, xor_1_out);
  xor xor_3 (out_5, and_2_out, and_1_out);
endmodule

module inc (
  input  in_1,
  output out_2,
  output out_3
);

  xor xor_1 (out_2, 1'b1, in_1);
  and and_1 (out_3, in_1, 1'b1);
endmodule

module dec (
  input  in_1,
  output out_2,
  output out_3
);

  wire not_1_out;

  not not_1 (not_1_out, 1'b1);
  xor xor_1 (out_2, 1'b1, in_1);
  and and_1 (out_3, not_1_out, in_1);
endmodule
