// Logisim project Exemplo0035.circ as structural Verilog: 4 circuits, main circuit main
module main (
  input  in_1,
  input  in_2,
  input  in_3,
  input  in_4,
  output G,
  output E,
  output L
);

  G g_1 (.in_1(in_2), .in_2(in_1), .in_3(in_4), .in_4(in_3), .out_5(G));
  E e_1 (.in_1(in_2), .in_2(in_1), .in_3(in_4), .in_4(in_3), .out_5(E));
  L l_1 (.in_1(in_2), .in_2(in_1), .in_3(in_4), .in_4(in_3), .out_5(L));

  // Notes on the sheet:
  //   Nome: Tiago Matta Machado Zaidan
  //   Matricula: 451620
  //   Exemplo0035
endmodule

module E (
  input  in_1,
  input  in_2,
  input  in_3,
  input  in_4,
  output out_5
);

  wire xnor_1_out, xnor_2_out;

  xnor xnor_1 (xnor_1_out, in_1, in_3);
  xnor xnor_2 (xnor_2_out, in_2, in_4);
  and and_1 (out_5, xnor_1_out, xnor_2_out);
endmodule

module G (
  input  in_1,
  input  in_2,
  input  in_3,
  input  in_4,
  output out_5
);

  wire and_1_out, and_2_out, and_3_out, not_1_out, not_2_out, or_1_out;

  and and_1 (and_1_out, in_1, not_1_out);
  not not_1 (not_1_out, in_3);
  or or_1 (or_1_out, in_2, not_2_out);
  and and_2 (and_2_out, and_1_out, or_1_out);
  or or_2 (out_5, and_2_out, and_3_out);
  not not_2 (not_2_out, in_4);
  and and_3 (and_3_out, in_2, not_2_out);
endmodule

module L (
  input  in_1,
  input  in_2,
  input  in_3,
  input  in_4,
  output out_5
);

  wire and_1_out, and_2_out, and_3_out, not_1_out, not_2_out, or_1_out;

  not not_1 (not_1_out, in_2);
  not not_2 (not_2_out, in_1);
  and and_1 (and_1_out, not_2_out, in_3);
  or or_1 (or_1_out, not_1_out, in_4);
  and and_2 (and_2_out, and_1_out, or_1_out);
  or or_2 (out_5, and_2_out, and_3_out);
  and and_3 (and_3_out, not_1_out, in_4);
endmodule
