// Logisim project EstudoDirigido05.circ as structural Verilog: 10 circuits, main circuit 1.Somador
// +
module _1_Somador (
  input  Cn,
  input  A,
  input  B,
  output S,
  output Cn_1
);

  wire and_1_out, and_2_out, xor_1_out;

  xor xor_1 (xor_1_out, A, B);
  and and_1 (and_1_out, A, B);
  and and_2 (and_2_out, Cn, xor_1_out);
  xor xor_2 (S, Cn, xor_1_out);
  or or_1 (Cn_1, and_2_out, and_1_out);

  // Notes on the sheet:
  //   Exercicio 01
  //   Wadson Ferreira - 460631
endmodule

// +-
module _1_SomaSub3 (
  input  Op,
  input  [2:0] A,
  input  [2:0] B,
  output [2:0] S,
  output Cn_3
);

  wire n1_somador_1_cn_1, n1_somador_2_cn_1, xor_1_out, xor_2_out, xor_3_out;

  _1_Somador u_1_somador_1 (.Cn(Op), .A(A[0]), .B(xor_1_out), .S(S[0]), .Cn_1(n1_somador_1_cn_1));
  xor xor_1 (xor_1_out, Op, B[0]);
  xor xor_2 (xor_2_out, Op, B[1]);
  _1_Somador u_1_somador_2 (.Cn(n1_somador_1_cn_1), .A(A[1]), .B(xor_2_out), .S(S[1]), .Cn_1(n1_somador_2_cn_1));
  xor xor_3 (xor_3_out, Op, B[2]);
  _1_Somador u_1_somador_3 (.Cn(n1_somador_2_cn_1), .A(A[2]), .B(xor_3_out), .S(S[2]), .Cn_1(Cn_3));

  // Notes on the sheet:
  //   Exercicio 01
  //   Wadson Ferreira - 460631
  //   Op=0 (Adição), Op=1 (Subtração)
endmodule

module _2_ZERO_flag (
  input  Op,
  input  [2:0] A,
  input  [2:0] B,
  output [2:0] S,
  output ZF,
  output Cn_3
);

  _1_SomaSub3 u_1_somasub3_1 (.Op(Op), .A(A), .B(B), .S(S), .Cn_3(Cn_3));
  nor nor_1 (ZF, S[2], S[1], S[0]);

  // Notes on the sheet:
  //   Exercicio 02
  //   Wadson Ferreira - 460631
  //   Op=0 (Adição), Op=1 (Subtração)
endmodule

module _3_Inc (
  input  [2:0] in_1,
  output [2:0] out_2
);

  _1_SomaSub3 u_1_somasub3_1 (.Op(1'b0), .A(in_1), .B(3'b001), .S(out_2));  // open: Cn_3

  // Notes on the sheet:
  //   Exercicio 03
  //   Wadson Ferreira - 460631
endmodule

// OVR
module _4_Carry_Overflow (
  input  Op,
  input  [2:0] A,
  input  [2:0] B,
  output [2:0] S,
  output Cn_3,
  output ZF,
  output OVR
);

  wire and_1_out, and_2_out, not_1_out, not_2_out, not_3_out;

  _1_SomaSub3 u_1_somasub3_1 (.Op(Op), .A(A), .B(B), .S(S), .Cn_3(Cn_3));
  nor nor_1 (ZF, S[0], S[1], S[2]);
  not not_1 (not_1_out, Op);
  not not_2 (not_2_out, A[2]);
  and and_1 (and_1_out, not_1_out, not_2_out, not_3_out, S[2]);
  not not_3 (not_3_out, B[2]);
  and and_2 (and_2_out, not_1_out, B[2], Op, S[2]);
  or or_1 (OVR, and_1_out, and_2_out);

  // Notes on the sheet:
  //   Exercicio 04
  //   Wadson Ferreira - 460631
  //   Op=0 (Adição), Op=1 (Subtração)
endmodule

// Sig
module _5_Sinal (
  input  Op,
  input  [2:0] A,
  input  [2:0] B,
  output [2:0] S,
  output Cn_3,
  output ZF,
  output OVR,
  output SA,
  output SB,
  output SS
);

  _4_Carry_Overflow u_4_carry_overflow_1 (.Op(Op), .A(A), .B(B), .S(S), .Cn_3(Cn_3), .ZF(ZF), .OVR(OVR));

  assign SA = A[2];
  assign SB = B[2];
  assign SS = S[2];

  // Notes on the sheet:
  //   Exercicio 05
  //   SA = Sinal de A
  //   SB = Sinal de B
  //   SS = Sinal da saida
  //   Wadson Ferreira - 460631
  //   Op=0 (Adição), Op=1 (Subtração)
endmodule

module _6_Dec (
  input  [2:0] in_1,
  output [2:0] out_2
);

  _1_SomaSub3 u_1_somasub3_1 (.Op(1'b1), .A(in_1), .B(3'b001), .S(out_2));  // open: Cn_3

  // Notes on the sheet:
  //   Exercicio 06
  //   Wadson Ferreira - 460631
endmodule

// C1
module _7_Comparador1bit (
  input  A,
  input  B,
  output A_B,
  output A_B_2,
  output A_B_3
);

  wire not_1_out, not_2_out;

  and and_1 (A_B, A, not_1_out);
  not not_1 (not_1_out, B);
  xnor xnor_1 (A_B_2, A, B);
  not not_2 (not_2_out, A);
  and and_2 (A_B_3, not_2_out, B);

  // Notes on the sheet:
  //   Exercicio 07
  //   Wadson Ferreira - 460631
endmodule

module _7_Comparador3bit (
  input  [2:0] A,
  input  [2:0] B,
  output A_B,
  output A_B_2,
  output A_B_3
);

  wire a_2_out, A_a_b, A_a_b_2, A_a_b_3, b_2_out, B_a_b, B_a_b_2, B_a_b_3, c_2_out, C_a_b, C_a_b_2, C_a_b_3,
       e_out, f_out, g_out, i_out;

  _7_Comparador1bit u_A (.A(A[2]), .B(B[2]), .A_B(A_a_b), .A_B_2(A_a_b_2), .A_B_3(A_a_b_3));
  _7_Comparador1bit u_B (.A(A[1]), .B(B[1]), .A_B(B_a_b), .A_B_2(B_a_b_2), .A_B_3(B_a_b_3));
  _7_Comparador1bit C (.A(A[0]), .B(B[0]), .A_B(C_a_b), .A_B_2(C_a_b_2), .A_B_3(C_a_b_3));
  and a_2 (a_2_out, A_a_b_2, B_a_b);
  // AND_Gate XX has open pins: in0=A_a_b_2, in1=B_a_b_2, out=open
  and b_2 (b_2_out, A_a_b_2, B_a_b_3);
  and c_2 (c_2_out, A_a_b_2, B_a_b_2, C_a_b);
  and d (A_B_2, A_a_b_2, B_a_b_2, C_a_b_2);
  and e (e_out, A_a_b_2, B_a_b_2, C_a_b_3);
  xor f (f_out, A[2], B[2]);
  or g (g_out, A_a_b, a_2_out, c_2_out);
  or i (i_out, A_a_b_3, b_2_out, e_out);
  xor h (A_B, f_out, g_out);
  xor j (A_B_3, f_out, i_out);

  // Notes on the sheet:
  //   Exercicio 07
  //   Wadson Ferreira - 460631
  //   Comparação por Lógica
endmodule

module \_7_ComparadorAritmético  (
  input  [2:0] A,
  input  [2:0] B,
  output A_B,
  output A_B_2,
  output A_B_3
);

  wire a_out, b_out, c_out, d_out, e_out, f_out, n5_sinal_1_sa, n5_sinal_1_sb, n5_sinal_1_ss, not_1_out,
       not_2_out, not_3_out, not_4_out;

  _5_Sinal u_5_sinal_1 (
    .Op(1'b1), .A(A), .B(B), .ZF(A_B_2), .SA(n5_sinal_1_sa), .SB(n5_sinal_1_sb), .SS(n5_sinal_1_ss));  // open: S, Cn_3, OVR
  not not_1 (not_1_out, n5_sinal_1_sa);
  not not_2 (not_2_out, n5_sinal_1_sb);
  not not_3 (not_3_out, n5_sinal_1_ss);
  not not_4 (not_4_out, A_B_2);
  and u_a (a_out, not_4_out, not_3_out, not_2_out, not_1_out);
  or g (A_B, a_out, f_out, d_out);
  and u_b (b_out, n5_sinal_1_ss, not_2_out, not_1_out);
  and c (c_out, n5_sinal_1_ss, n5_sinal_1_sb, n5_sinal_1_sa);
  or h (A_B_3, b_out, e_out, c_out);
  and e (e_out, not_2_out, n5_sinal_1_sa);
  and d (d_out, not_3_out, n5_sinal_1_sb, n5_sinal_1_sa, not_4_out);
  and f (f_out, not_1_out, n5_sinal_1_sb);

  // Notes on the sheet:
  //   Exercicio 07
  //   Wadson Ferreira - 460631
  //   Comparação por Subtração
endmodule
