// Logisim project Exemplo0033.circ as structural Verilog: 3 circuits, main circuit sum/diff
// AU
module sum_diff (
  input  inc,
  input  [2:0] a,
  input  [2:0] b,
  input  carryIn,
  output [2:0] sum_diff,
  output carryOut,
  output Flag,
  output Sinal,
  output Overflow
);

  wire inc_1_out_5, inc_1_out_6, inc_1_out_7, soma_1_p5, soma_2_p5, soma_3_p5, xor_1_out, xor_2_out,
       xor_3_out, xor_5_out;

  inc inc_1 (
    .in_2(a[0]), .in_3(a[1]), .in_4(a[2]), .in_1(inc), .out_5(inc_1_out_5), .out_6(inc_1_out_6),
    .out_7(inc_1_out_7));
  xor xor_1 (xor_1_out, carryIn, b[0]);
  xor xor_2 (xor_2_out, carryIn, b[1]);
  xor xor_3 (xor_3_out, carryIn, b[2]);
  // soma soma_1: pin names not known; wires that end beside it: xor_1_out, inc_1_out_5, carryIn, sum_diff[0], soma_1_p5
  // soma soma_2: pin names not known; wires that end beside it: xor_2_out, inc_1_out_6, soma_1_p5, sum_diff[1], soma_2_p5
  // soma soma_3: pin names not known; wires that end beside it: inc_1_out_7, xor_3_out, soma_2_p5, Sinal, soma_3_p5
  xor xor_4 (carryOut, soma_3_p5, carryIn);
  nor nor_1 (Flag, sum_diff[0], sum_diff[1], Sinal);
  or or_1 (Overflow, carryOut, xor_5_out);
  xor xor_5 (xor_5_out, soma_2_p5, soma_3_p5);

  assign sum_diff[2] = Sinal;

  // Notes on the sheet:
  //   carryIn
  //   0      soma
  //   1       diferença
endmodule

module HA (
  input  in_1,
  input  in_2,
  output out_3,
  output out_4
);

  xor xor_1 (out_3, in_1, in_2);
  and and_1 (out_4, in_1, in_2);
endmodule

// HA
module inc (
  input  in_1,
  input  in_2,
  input  in_3,
  input  in_4,
  output out_5,
  output out_6,
  output out_7
);

  wire ha_1_out_4, ha_2_out_4;

  HA ha_1 (.in_1(in_1), .in_2(in_2), .out_3(out_5), .out_4(ha_1_out_4));
  HA ha_2 (.in_1(ha_1_out_4), .in_2(in_3), .out_3(out_6), .out_4(ha_2_out_4));
  HA ha_3 (.in_1(ha_2_out_4), .in_2(in_4), .out_3(out_7));  // open: out_4
endmodule
