// Logisim project Exemplo0035.circ as structural Verilog: 2 circuits, main circuit sum/diff
// AU
module sum_diff (
  input  [2:0] a,
  input  [2:0] b,
  input  carryIn,
  output [2:0] sum_diff,
  output carryOut,
  output Flag,
  output sinal,
  output Overflow
);

  wire soma_1_p5, soma_2_p5, soma_3_p5, xor_1_out, xor_2_out, xor_3_out, xor_5_out;

  xor xor_1 (xor_1_out, carryIn, b[0]);
  xor xor_2 (xor_2_out, carryIn, b[1]);
  xor xor_3 (xor_3_out, carryIn, b[2]);
  // soma soma_1: pin names not known; wires that end beside it: xor_1_out, a[0], carryIn, sum_diff[0], soma_1_p5
  // soma soma_2: pin names not known; wires that end beside it: xor_2_out, a[1], soma_1_p5, sum_diff[1], soma_2_p5
  // soma soma_3: pin names not known; wires that end beside it: a[2], xor_3_out, soma_2_p5, sum_diff[2], soma_3_p5
  xor xor_4 (carryOut, soma_3_p5, carryIn);
  nor nor_1 (Flag, sum_diff[0], sum_diff[1], sum_diff[2]);
  buf buffer_1 (sinal, sum_diff[2]);
  or or_1 (Overflow, carryOut, xor_5_out);
  xor xor_5 (xor_5_out, soma_2_p5, soma_3_p5);

  // Notes on the sheet:
  //   carryIn
  //   0      soma
  //   1       diferença
endmodule

module compac (
  input  [2:0] a,
  input  [2:0] b,
  input  carryIn,
  output [2:0] sum_diff,
  output carryOut,
  output flag,
  output overflow
);

  sum_diff sum_diff_1 (
    .a(a), .b(b), .carryIn(carryIn), .sum_diff(sum_diff), .carryOut(carryOut), .Flag(flag), .sinal(overflow));  // open: Overflow
endmodule
