// Logisim project Exemplo0052 -.circ as structural Verilog: 1 circuit, main circuit main
module main (
  input  CLK,
  input  X,
  input  RESET,
  output out_4
);

  wire and_1_out, and_2_out, d_ff_1_q, d_ff_2_q, d_ff_2_qn, d_ff_3_q, d_ff_3_qn, d_ff_4_q, not_1_out,
       not_2_out;

  D_Flip_Flop d_ff_1 (.clk(CLK), .D(X), .Q(d_ff_1_q), .reset(RESET));  // open: Qn, preset, en
  and and_1 (and_1_out, d_ff_1_q, d_ff_4_q, d_ff_2_qn, d_ff_3_qn);
  D_Flip_Flop d_ff_2 (.clk(CLK), .D(d_ff_1_q), .Q(d_ff_2_q), .Qn(d_ff_2_qn), .reset(RESET));  // open: preset, en
  or or_1 (out_4, and_1_out, and_2_out);
  D_Flip_Flop d_ff_3 (.clk(CLK), .D(d_ff_2_q), .Q(d_ff_3_q), .Qn(d_ff_3_qn), .reset(RESET));  // open: preset, en
  not not_1 (not_1_out, d_ff_2_q);
  not not_2 (not_2_out, d_ff_4_q);
  and and_2 (and_2_out, d_ff_1_q, not_1_out, d_ff_3_q, not_2_out);
  D_Flip_Flop d_ff_4 (.clk(CLK), .D(d_ff_3_q), .Q(d_ff_4_q), .reset(RESET));  // open: Qn, preset, en

  // Notes on the sheet:
  //   1-reconhece-1010   e
  //    1001001
endmodule
