// Logisim project Exemplo0054 -.circ as structural Verilog: 1 circuit, main circuit main
module main (
  input  CLK,
  input  X,
  input  RESET,
  output Y
);

  wire d_ff_1_q, d_ff_1_qn, d_ff_2_q, d_ff_3_q, d_ff_4_q;

  D_Flip_Flop d_ff_1 (.clk(CLK), .D(X), .Q(d_ff_1_q), .Qn(d_ff_1_qn), .reset(RESET));  // open: preset, en
  D_Flip_Flop d_ff_2 (.clk(CLK), .D(d_ff_1_q), .Q(d_ff_2_q), .reset(RESET));  // open: Qn, preset, en
  and and_1 (Y, d_ff_1_qn, d_ff_2_q, d_ff_3_q, d_ff_4_q);
  D_Flip_Flop d_ff_3 (.clk(CLK), .D(d_ff_2_q), .Q(d_ff_3_q), .reset(RESET));  // open: Qn, preset, en
  D_Flip_Flop d_ff_4 (.clk(CLK), .D(d_ff_3_q), .Q(d_ff_4_q), .reset(RESET));  // open: Qn, preset, en
endmodule
