// Logisim project Exemplo0055 -.circ as structural Verilog: 1 circuit, main circuit main
module main (
  input  CLK,
  input  CLK_2,
  input  X,
  input  X_2,
  input  RESET,
  input  RESET_2,
  output Y,
  output Y_2
);

  wire d_ff_1_q, d_ff_1_qn, d_ff_2_q, d_ff_3_q, d_ff_4_q, d_ff_5_q, d_ff_5_qn, d_ff_6_q, d_ff_6_qn, d_ff_7_q,
       d_ff_7_qn, d_ff_8_qn, or_1_out, xnor_1_out;

  D_Flip_Flop d_ff_1 (.clk(CLK), .D(X), .Q(d_ff_1_q), .Qn(d_ff_1_qn), .reset(RESET));  // open: preset, en
  xnor xnor_1 (xnor_1_out, d_ff_1_qn, d_ff_1_q);
  D_Flip_Flop d_ff_2 (.clk(CLK), .D(d_ff_1_q), .Q(d_ff_2_q), .reset(RESET));  // open: Qn, preset, en
  D_Flip_Flop d_ff_3 (.clk(CLK), .D(d_ff_2_q), .Q(d_ff_3_q), .reset(RESET));  // open: Qn, preset, en
  nor nor_1 (Y, xnor_1_out, d_ff_2_q, d_ff_3_q, d_ff_4_q);
  D_Flip_Flop d_ff_4 (.clk(CLK), .D(d_ff_3_q), .Q(d_ff_4_q), .reset(RESET));  // open: Qn, preset, en
  D_Flip_Flop d_ff_5 (.clk(CLK_2), .D(X_2), .Q(d_ff_5_q), .Qn(d_ff_5_qn), .reset(RESET_2));  // open: preset, en
  or or_1 (or_1_out, d_ff_5_qn, d_ff_5_q);
  D_Flip_Flop d_ff_6 (.clk(CLK_2), .D(d_ff_5_q), .Q(d_ff_6_q), .Qn(d_ff_6_qn), .reset(RESET_2));  // open: preset, en
  and and_1 (Y_2, or_1_out, d_ff_6_qn, d_ff_7_qn, d_ff_8_qn);
  D_Flip_Flop d_ff_7 (.clk(CLK_2), .D(d_ff_6_q), .Q(d_ff_7_q), .Qn(d_ff_7_qn), .reset(RESET_2));  // open: preset, en
  D_Flip_Flop d_ff_8 (.clk(CLK_2), .D(d_ff_7_q), .Qn(d_ff_8_qn), .reset(RESET_2));  // open: Q, preset, en

  // Notes on the sheet:
  //   x000
  //   x = 0 ou 1
  //   x000
  //   x = 0 ou 1
endmodule
