// Logisim project Exemplo0056 -.circ as structural Verilog: 1 circuit, main circuit main
module main (
  input  clk,
  input  x,
  input  reset,
  output y
);

  wire and_1_out, and_2_out, d_ff_1_q, d_ff_1_qn, d_ff_2_q, d_ff_2_qn, d_ff_3_q, d_ff_3_qn;

  D_Flip_Flop d_ff_1 (.clk(clk), .D(x), .Q(d_ff_1_q), .Qn(d_ff_1_qn), .reset(reset));  // open: preset, en
  D_Flip_Flop d_ff_2 (.clk(clk), .D(d_ff_1_q), .Q(d_ff_2_q), .Qn(d_ff_2_qn), .reset(reset));  // open: preset, en
  D_Flip_Flop d_ff_3 (.clk(clk), .D(d_ff_2_q), .Q(d_ff_3_q), .Qn(d_ff_3_qn), .reset(reset));  // open: preset, en
  and and_1 (and_1_out, d_ff_2_qn, d_ff_1_qn, d_ff_3_qn);
  or or1 (y, and_1_out, and_2_out);
  and and_2 (and_2_out, d_ff_3_q, d_ff_2_q, d_ff_1_q);

  // Notes on the sheet:
  //   NAND1
  //   NAND2
endmodule
