// Logisim project Exemplo0052.circ as structural Verilog: 1 circuit, main circuit main
module main (
  input  X,
  input  clear,
  output s
);

  wire clock_out, d_ff_1_q, d_ff_2_q, d_ff_2_qn, d_ff_3_q, d_ff_3_qn, d_ff_4_q;

  Clock clock (.out(clock_out));
  D_Flip_Flop d_ff_1 (.clk(clock_out), .D(X), .Q(d_ff_1_q), .reset(clear));  // open: Qn, preset, en
  and and_1 (s, d_ff_1_q, d_ff_2_qn, d_ff_3_qn, d_ff_4_q);
  D_Flip_Flop d_ff_2 (.clk(clock_out), .D(d_ff_1_q), .Q(d_ff_2_q), .Qn(d_ff_2_qn), .reset(clear));  // open: preset, en
  D_Flip_Flop d_ff_3 (.clk(clock_out), .D(d_ff_2_q), .Q(d_ff_3_q), .Qn(d_ff_3_qn), .reset(clear));  // open: preset, en
  D_Flip_Flop d_ff_4 (.clk(clock_out), .D(d_ff_3_q), .Q(d_ff_4_q), .reset(clear));  // open: Qn, preset, en

  // Notes on the sheet:
  //   Mealy1001
endmodule
