// Logisim project Exemplo0053.circ as structural Verilog: 1 circuit, main circuit main
module main (
  input  X,
  input  clear,
  output s
);

  wire and_1_out, and_2_out, clock_out, d_ff_1_q, d_ff_2_q, d_ff_2_qn, d_ff_3_q, d_ff_3_qn, d_ff_4_q,
       not_1_out, or_1_out;

  Clock clock (.out(clock_out));
  D_Flip_Flop d_ff_1 (.clk(clock_out), .D(X), .Q(d_ff_1_q), .reset(or_1_out));  // open: Qn, preset, en
  or or_1 (or_1_out, clear, and_2_out);
  D_Flip_Flop d_ff_2 (
    .clk(clock_out), .D(d_ff_1_q), .Q(d_ff_2_q), .Qn(d_ff_2_qn), .reset(or_1_out));  // open: preset, en
  D_Flip_Flop d_ff_3 (
    .clk(clock_out), .D(d_ff_2_q), .Q(d_ff_3_q), .Qn(d_ff_3_qn), .reset(or_1_out));  // open: preset, en
  and and_1 (and_1_out, d_ff_4_q, d_ff_3_qn, d_ff_2_qn, d_ff_1_q);
  not not_1 (not_1_out, clock_out);
  D_Flip_Flop d_ff_4 (.clk(clock_out), .D(d_ff_3_q), .Q(d_ff_4_q), .reset(or_1_out));  // open: Qn, preset, en
  and and_2 (and_2_out, not_1_out, s);
  D_Flip_Flop d_ff_5 (.clk(not_1_out), .Q(s), .preset(and_1_out), .reset(or_1_out));  // open: D, Qn, en

  // Notes on the sheet:
  //   Moore1001
endmodule
