// Logisim project Exemplo0054.circ as structural Verilog: 1 circuit, main circuit main
module main (
  input  X,
  input  clear,
  output s
);

  wire and_1_out, clock_out, d_ff_1_q, d_ff_2_q, d_ff_3_q, d_ff_3_qn, d_ff_4_qn, not_1_out;

  Clock clock (.out(clock_out));
  and and_1 (and_1_out, not_1_out, clock_out);
  D_Flip_Flop d_ff_1 (.clk(and_1_out), .D(X), .Q(d_ff_1_q), .en(not_1_out), .reset(clear));  // open: Qn, preset
  not not_1 (not_1_out, s);
  D_Flip_Flop d_ff_2 (.clk(and_1_out), .D(d_ff_1_q), .Q(d_ff_2_q), .en(not_1_out), .reset(clear));  // open: Qn, preset
  D_Flip_Flop d_ff_3 (
    .clk(and_1_out), .D(d_ff_2_q), .Q(d_ff_3_q), .Qn(d_ff_3_qn), .en(not_1_out), .reset(clear));  // open: preset
  and and_2 (s, d_ff_4_qn, d_ff_3_qn, d_ff_2_q, d_ff_1_q);
  D_Flip_Flop d_ff_4 (.clk(and_1_out), .D(d_ff_3_q), .Qn(d_ff_4_qn), .en(not_1_out), .reset(clear));  // open: Q, preset

  // Notes on the sheet:
  //   Sequencia 1100
endmodule
