// Logisim project Exemplo0056.circ as structural Verilog: 1 circuit, main circuit main
module main (
  input  X,
  input  clear,
  output s
);

  wire and_1_out, clock_out, d_ff_1_q, d_ff_2_q, d_ff_3_q, nor_1_out;

  Clock clock (.out(clock_out));
  D_Flip_Flop d_ff_1 (.clk(clock_out), .D(X), .Q(d_ff_1_q), .reset(clear));  // open: Qn, preset, en
  D_Flip_Flop d_ff_2 (.clk(clock_out), .D(d_ff_1_q), .Q(d_ff_2_q), .reset(clear));  // open: Qn, preset, en
  nor nor_1 (nor_1_out, d_ff_3_q, d_ff_2_q, d_ff_1_q);
  or or_1 (s, nor_1_out, and_1_out);
  and and_1 (and_1_out, d_ff_3_q, d_ff_2_q, d_ff_1_q);
  D_Flip_Flop d_ff_3 (.clk(clock_out), .D(d_ff_2_q), .Q(d_ff_3_q), .reset(clear));  // open: Qn, preset, en

  // Notes on the sheet:
  //   Sequencia 000 ou 111
endmodule
