// Logisim project Circuitos.circ as structural Verilog: 3 circuits, main circuit Exemplo0052
module Exemplo0052 (
  input  Entrada,
  input  Reset,
  output S
);

  wire Clock_out, d_ff_1_q, d_ff_2_q, d_ff_3_q, d_ff_4_q;

  Clock Clock (.out(Clock_out));
  D_Flip_Flop d_ff_1 (.clk(Clock_out), .D(Entrada), .Q(d_ff_1_q), .reset(Reset));  // open: Qn, preset, en
  D_Flip_Flop d_ff_2 (.clk(Clock_out), .D(d_ff_1_q), .Q(d_ff_2_q), .reset(Reset));  // open: Qn, preset, en
  and and_1 (S, ~d_ff_2_q, d_ff_1_q, ~d_ff_4_q, d_ff_3_q);  // AND_Gate
  D_Flip_Flop d_ff_3 (.clk(Clock_out), .D(d_ff_2_q), .Q(d_ff_3_q), .reset(Reset));  // open: Qn, preset, en
  D_Flip_Flop d_ff_4 (.clk(Clock_out), .D(d_ff_3_q), .Q(d_ff_4_q), .reset(Reset));  // open: Qn, preset, en

  // Notes on the sheet:
  //   Exemplo0052 - Djonatas Tulio Rodrigues Costa - 440954
endmodule

module Exemplo0053 (
  input  Entrada,
  input  Reset,
  output S
);

  wire and_1_out, Clock_out, d_ff_1_q, d_ff_2_q, d_ff_3_q, d_ff_4_q;

  Clock Clock (.out(Clock_out));
  D_Flip_Flop d_ff_1 (.clk(Clock_out), .D(Entrada), .Q(d_ff_1_q), .reset(Reset));  // open: Qn, preset, en
  D_Flip_Flop d_ff_2 (.clk(Clock_out), .D(d_ff_1_q), .Q(d_ff_2_q), .reset(Reset));  // open: Qn, preset, en
  D_Flip_Flop d_ff_3 (.clk(Clock_out), .D(d_ff_2_q), .Q(d_ff_3_q), .reset(Reset));  // open: Qn, preset, en
  D_Flip_Flop d_ff_4 (.clk(Clock_out), .D(d_ff_3_q), .Q(d_ff_4_q), .reset(Reset));  // open: Qn, preset, en
  D_Flip_Flop d_ff_5 (.clk(Clock_out), .D(and_1_out), .Q(S), .reset(Reset));  // open: Qn, preset, en
  and and_1 (and_1_out, ~d_ff_4_q, d_ff_3_q, ~d_ff_2_q, d_ff_1_q);  // AND_Gate

  // Notes on the sheet:
  //   Exemplo0053 - Djonatas Tulio Rodrigues Costa - 440954
endmodule

module Exemplo0054 (
  input  Entrada,
  input  Reset,
  output S
);

  wire Clock_out, d_ff_1_q, d_ff_2_q, d_ff_3_q, d_ff_4_q;

  Clock Clock (.out(Clock_out));
  D_Flip_Flop d_ff_1 (.clk(Clock_out), .D(Entrada), .Q(d_ff_1_q), .reset(Reset));  // open: Qn, preset, en
  D_Flip_Flop d_ff_2 (.clk(Clock_out), .D(d_ff_1_q), .Q(d_ff_2_q), .reset(Reset));  // open: Qn, preset, en
  and and_1 (S, d_ff_2_q, d_ff_1_q, ~d_ff_4_q, ~d_ff_3_q);  // AND_Gate
  D_Flip_Flop d_ff_3 (.clk(Clock_out), .D(d_ff_2_q), .Q(d_ff_3_q), .reset(Reset));  // open: Qn, preset, en
  D_Flip_Flop d_ff_4 (.clk(Clock_out), .D(d_ff_3_q), .Q(d_ff_4_q), .reset(Reset));  // open: Qn, preset, en

  // Notes on the sheet:
  //   Exemplo0054 - Djonatas Tulio Rodrigues Costa - 440954
endmodule
