// Logisim project Exemplo0053.circ as structural Verilog: 1 circuit, main circuit main
module main (
  input  x,
  input  Reset,
  output s
);

  wire AND_out, Clk_out, d_ff_1_q, d_ff_2_q, d_ff_3_q, d_ff_4_q, not_1_out, not_2_out;

  Clock Clk (.out(Clk_out));
  D_Flip_Flop d_ff_1 (.clk(Clk_out), .Q(d_ff_1_q), .reset(Reset));  // open: D, Qn, preset, en
  D_Flip_Flop d_ff_2 (.clk(Clk_out), .D(d_ff_1_q), .Q(d_ff_2_q), .reset(Reset));  // open: Qn, preset, en
  not not_1 (not_1_out, d_ff_2_q);
  and AND (AND_out, d_ff_1_q, not_1_out, not_2_out, d_ff_4_q);
  D_Flip_Flop d_ff_3 (.clk(Clk_out), .D(d_ff_2_q), .Q(d_ff_3_q), .reset(Reset));  // open: Qn, preset, en
  not not_2 (not_2_out, d_ff_3_q);
  D_Flip_Flop d_ff_4 (.clk(Clk_out), .D(d_ff_3_q), .Q(d_ff_4_q), .reset(Reset));  // open: Qn, preset, en
  D_Flip_Flop d_ff_5 (.clk(Clk_out), .D(AND_out), .Q(s));  // open: Qn, preset, en, reset
endmodule
