// Logisim project Exemplo0052.circ as structural Verilog: 1 circuit, main circuit main
module main (
  input  in_1,
  input  in_2,
  output out_3
);

  wire and_1_out, and_2_out, clock_1_out, d_ff_1_q, d_ff_2_q, d_ff_3_q, d_ff_4_q, d_ff_5_q, d_ff_6_q,
       d_ff_7_q, d_ff_8_q, d_ff_9_q, d_ff_10_q, d_ff_11_q, not_1_out, not_2_out, not_3_out, not_4_out,
       not_5_out, not_6_out;

  Clock clock_1 (.out(clock_1_out));
  D_Flip_Flop d_ff_1 (.clk(clock_1_out), .D(d_ff_3_q), .Q(d_ff_1_q), .reset(in_2));  // open: Qn, preset, en
  D_Flip_Flop d_ff_2 (.clk(clock_1_out), .D(d_ff_4_q), .Q(d_ff_2_q), .reset(in_2));  // open: Qn, preset, en
  D_Flip_Flop d_ff_3 (.clk(clock_1_out), .D(d_ff_5_q), .Q(d_ff_3_q), .reset(in_2));  // open: Qn, preset, en
  not not_1 (not_1_out, d_ff_3_q);
  D_Flip_Flop d_ff_4 (.clk(clock_1_out), .D(d_ff_7_q), .Q(d_ff_4_q), .reset(in_2));  // open: Qn, preset, en
  D_Flip_Flop d_ff_5 (.clk(clock_1_out), .D(d_ff_6_q), .Q(d_ff_5_q), .reset(in_2));  // open: Qn, preset, en
  not not_2 (not_2_out, d_ff_5_q);
  not not_3 (not_3_out, d_ff_4_q);
  and and_1 (and_1_out, d_ff_2_q, not_3_out, d_ff_7_q, not_6_out);
  D_Flip_Flop d_ff_6 (.clk(clock_1_out), .D(d_ff_8_q), .Q(d_ff_6_q), .reset(in_2));  // open: Qn, preset, en
  D_Flip_Flop d_ff_7 (.clk(clock_1_out), .D(d_ff_10_q), .Q(d_ff_7_q), .reset(in_2));  // open: Qn, preset, en
  D_Flip_Flop d_ff_8 (.clk(clock_1_out), .D(d_ff_9_q), .Q(d_ff_8_q), .reset(in_2));  // open: Qn, preset, en
  not not_4 (not_4_out, d_ff_8_q);
  D_Flip_Flop d_ff_9 (.clk(clock_1_out), .D(d_ff_11_q), .Q(d_ff_9_q), .reset(in_2));  // open: Qn, preset, en
  not not_5 (not_5_out, d_ff_9_q);
  D_Flip_Flop d_ff_10 (.clk(clock_1_out), .D(in_1), .Q(d_ff_10_q), .reset(in_2));  // open: Qn, preset, en
  not not_6 (not_6_out, d_ff_10_q);
  D_Flip_Flop d_ff_11 (.clk(clock_1_out), .D(in_1), .Q(d_ff_11_q), .reset(in_2));  // open: Qn, preset, en
  and and_2 (and_2_out, d_ff_11_q, d_ff_6_q, d_ff_1_q, not_5_out, not_1_out, not_2_out, not_4_out);
  or or_1 (out_3, and_1_out, and_2_out);

  // Notes on the sheet:
  //   MATRICULA: 451620
  //   NOME: TIAGO MATTA MACHADO ZAIDAN
endmodule
