// Logisim project Exemplo0055.circ as structural Verilog: 1 circuit, main circuit main
module main (
  input  in_1,
  input  in_2,
  output out_3
);

  wire clock_1_out, d_ff_1_q, d_ff_2_q, d_ff_3_q, d_ff_4_q, not_1_out, not_2_out, not_3_out;

  Clock clock_1 (.out(clock_1_out));
  D_Flip_Flop d_ff_1 (.clk(clock_1_out), .D(d_ff_2_q), .Q(d_ff_1_q), .reset(in_2));  // open: Qn, preset, en
  D_Flip_Flop d_ff_2 (.clk(clock_1_out), .D(d_ff_3_q), .Q(d_ff_2_q), .reset(in_2));  // open: Qn, preset, en
  not not_1 (not_1_out, d_ff_2_q);
  D_Flip_Flop d_ff_3 (.clk(clock_1_out), .D(d_ff_4_q), .Q(d_ff_3_q), .reset(in_2));  // open: Qn, preset, en
  not not_2 (not_2_out, d_ff_3_q);
  and and_1 (out_3, not_1_out, not_2_out, not_3_out);
  D_Flip_Flop d_ff_4 (.clk(clock_1_out), .D(in_1), .Q(d_ff_4_q), .reset(in_2));  // open: Qn, preset, en
  not not_3 (not_3_out, d_ff_4_q);

  // Notes on the sheet:
  //   MATRICULA: 451620
  //   NOME: TIAGO MATTA MACHADO ZAIDAN
endmodule
