// Logisim project Exemplo0052.circ as structural Verilog: 2 circuits, main circuit Mealy
// M
module Mealy (
  input  Clock,
  input  Entrada,
  input  Reset,
  output Saida
);

  wire and_1_out, and_2_out, and_3_out, d_ff_1_q, d_ff_1_qn, d_ff_2_q, d_ff_3_q, d_ff_4_q, d_ff_6_q,
       nand_1_out, not_1_out, not_2_out, not_3_out, not_4_out, or_1_out;

  nand nand_1 (nand_1_out, d_ff_2_q, d_ff_1_qn, not_1_out);
  and and_1 (and_1_out, nand_1_out, Clock);
  not not_1 (not_1_out, Entrada);
  D_Flip_Flop d_ff_1 (
    .clk(and_1_out), .D(Entrada), .Q(d_ff_1_q), .Qn(d_ff_1_qn), .reset(or_1_out));  // open: preset, en
  D_Flip_Flop d_ff_2 (.clk(and_1_out), .D(d_ff_1_q), .Q(d_ff_2_q), .reset(or_1_out));  // open: Qn, preset, en
  or or_1 (or_1_out, Reset, and_2_out);
  and and_2 (and_2_out, not_2_out, and_3_out);
  not not_2 (not_2_out, and_1_out);
  D_Flip_Flop d_ff_3 (.clk(and_1_out), .D(d_ff_2_q), .Q(d_ff_3_q), .reset(or_1_out));  // open: Qn, preset, en
  D_Flip_Flop d_ff_4 (.clk(and_1_out), .D(d_ff_3_q), .Q(d_ff_4_q), .reset(or_1_out));  // open: Qn, preset, en
  not not_3 (not_3_out, d_ff_3_q);
  not not_4 (not_4_out, d_ff_1_q);
  and and_3 (and_3_out, d_ff_4_q, not_3_out, d_ff_2_q, not_4_out);
  D_Flip_Flop #(.trigger("falling")) d_ff_5 (
    .clk(not_2_out), .D(d_ff_6_q), .Q(Saida), .reset(or_1_out));  // open: Qn, preset, en
  D_Flip_Flop d_ff_6 (.clk(not_2_out), .D(and_3_out), .Q(d_ff_6_q));  // open: Qn, preset, en, reset

  // Notes on the sheet:
  //   Wadson Ferreira
  //   460631
  //   Garante que o clock não afetará os flip-flop
  //   quando a entrada for uma interseção
  //   Atua como mestre-escravo
  //   para garantir o sinal da saída
endmodule

module Exemplo0052 (
  input  Clear,
  input  Reset,
  output Saida
);

  wire Clock_out;
  wire [6:0] keyboard_1_data;

  Clock Clock (.out(Clock_out));
  Keyboard #(.trigger("falling")) keyboard_1 (.clk(Clock_out), .clr(Clear), .data(keyboard_1_data));  // open: re, avail
  Mealy mealy_1 (.Clock(Clock_out), .Entrada(keyboard_1_data[0]), .Reset(Reset), .Saida(Saida));

  // Notes on the sheet:
  //   Wadson Ferreira
  //   460631
  //   Reconhecer 1010 com interseção
endmodule
