// Logisim project Exemplo0054.circ as structural Verilog: 2 circuits, main circuit Mealy
// M
module Mealy (
  input  Clock,
  input  Entrada,
  input  Reset,
  output Saida
);

  wire and_1_out, and_2_out, d_ff_1_q, d_ff_2_q, d_ff_3_q, d_ff_4_q, d_ff_5_qn, not_1_out, not_2_out;

  and and_1 (and_1_out, d_ff_5_qn, Clock);
  D_Flip_Flop d_ff_1 (.clk(and_1_out), .D(Entrada), .Q(d_ff_1_q), .reset(Reset));  // open: Qn, preset, en
  D_Flip_Flop d_ff_2 (.clk(and_1_out), .D(d_ff_1_q), .Q(d_ff_2_q), .reset(Reset));  // open: Qn, preset, en
  D_Flip_Flop d_ff_3 (.clk(and_1_out), .D(d_ff_2_q), .Q(d_ff_3_q), .reset(Reset));  // open: Qn, preset, en
  D_Flip_Flop d_ff_4 (.clk(and_1_out), .D(d_ff_3_q), .Q(d_ff_4_q), .reset(Reset));  // open: Qn, preset, en
  not not_1 (not_1_out, d_ff_2_q);
  not not_2 (not_2_out, d_ff_1_q);
  and and_2 (and_2_out, d_ff_4_q, d_ff_3_q, not_1_out, not_2_out);
  D_Flip_Flop d_ff_5 (.clk(and_2_out), .D(and_2_out), .Q(Saida), .Qn(d_ff_5_qn), .reset(Reset));  // open: preset, en

  // Notes on the sheet:
  //   Wadson Ferreira
  //   460631
endmodule

module Exemplo0054 (
  input  Clear,
  input  Reset,
  output Saida
);

  wire Clock_out;
  wire [6:0] keyboard_1_data;

  Clock Clock (.out(Clock_out));
  Keyboard #(.trigger("falling")) keyboard_1 (.clk(Clock_out), .clr(Clear), .data(keyboard_1_data));  // open: re, avail
  Mealy mealy_1 (.Clock(Clock_out), .Entrada(keyboard_1_data[0]), .Reset(Reset), .Saida(Saida));

  // Notes on the sheet:
  //   Wadson Ferreira
  //   460631
  //   Reconhecer apenas a primeira ocorrência de 1100
endmodule
