// Logisim project Exemplo0056.circ as structural Verilog: 2 circuits, main circuit Mealy
// M
module Mealy (
  input  CLK,
  input  Data,
  input  Reset,
  output Saida
);

  wire and_1_out, and_2_out, and_3_out, d_ff_1_q, d_ff_1_qn, d_ff_2_q, d_ff_2_qn, d_ff_3_q, d_ff_3_qn,
       not_1_out, not_2_out, or_1_out;
  wire [1:0] adder_1_out, register_1_q;

  Adder #(.width(2)) adder_1 (.a(2'b00), .b(register_1_q), .out(adder_1_out), .cin(CLK));  // open: cout
  D_Flip_Flop d_ff_1 (.clk(CLK), .D(Data), .Q(d_ff_1_q), .Qn(d_ff_1_qn), .reset(Reset));  // open: preset, en
  Register #(.width(2)) register_1 (.D(adder_1_out), .Q(register_1_q), .clk(not_1_out), .clr(Reset));  // open: en
  not not_1 (not_1_out, CLK);
  D_Flip_Flop d_ff_2 (.clk(CLK), .D(d_ff_1_q), .Q(d_ff_2_q), .Qn(d_ff_2_qn), .reset(Reset));  // open: preset, en
  and and_1 (and_1_out, register_1_q[0], register_1_q[1]);
  D_Flip_Flop d_ff_3 (.clk(CLK), .D(d_ff_2_q), .Q(d_ff_3_q), .Qn(d_ff_3_qn), .reset(Reset));  // open: preset, en
  and and_2 (and_2_out, and_1_out, d_ff_1_q, d_ff_2_q, d_ff_3_q);
  and and_3 (and_3_out, and_1_out, d_ff_1_qn, d_ff_2_qn, d_ff_3_qn);
  or or_1 (or_1_out, and_2_out, and_3_out);
  not not_2 (not_2_out, CLK);
  D_Flip_Flop d_ff_4 (.clk(not_2_out), .D(or_1_out), .Q(Saida), .reset(Reset));  // open: Qn, preset, en

  // Notes on the sheet:
  //   Wadson Ferreira
  //   460631
  //   de tres entradas
  //   Garante a resposta apenas depois
endmodule

module Exemplo0056 (
  input  Clear,
  output Encontrado
);

  wire Clock_out;
  wire [6:0] keyboard_1_data;

  Clock Clock (.out(Clock_out));
  Keyboard keyboard_1 (.clk(Clock_out), .clr(Clear), .data(keyboard_1_data));  // open: re, avail
  Mealy mealy_1 (.CLK(Clock_out), .Data(keyboard_1_data[0]), .Reset(Clear), .Saida(Encontrado));

  // Notes on the sheet:
  //   Wadson Ferreira
  //   460631
endmodule
