// Logisim project Exemplo0053(2).circ as structural Verilog: 1 circuit, main circuit main
module main (
  input  \input ,
  input  clear,
  output \output 
);

  wire and_1_out, and_2_out, clk_out, clock_1_out, d_ff_1_q, d_ff_2_q, d_ff_2_qn, d_ff_3_q, d_ff_3_qn,
       d_ff_4_q, d_ff_5_q, not_1_out, or_1_out;

  Clock #(.highDuration(2), .lowDuration(2)) clk (.out(clk_out));
  or or_1 (or_1_out, clear, and_2_out);
  D_Flip_Flop d_ff_1 (.clk(clk_out), .D(\input ), .Q(d_ff_1_q), .reset(or_1_out));  // open: Qn, preset, en
  D_Flip_Flop d_ff_2 (.clk(clk_out), .D(d_ff_1_q), .Q(d_ff_2_q), .Qn(d_ff_2_qn), .reset(or_1_out));  // open: preset, en
  D_Flip_Flop d_ff_3 (.clk(clk_out), .D(d_ff_2_q), .Q(d_ff_3_q), .Qn(d_ff_3_qn), .reset(or_1_out));  // open: preset, en
  not not_1 (not_1_out, clk_out);
  D_Flip_Flop d_ff_4 (.clk(clk_out), .D(d_ff_3_q), .Q(d_ff_4_q), .reset(or_1_out));  // open: Qn, preset, en
  and and_1 (and_1_out, d_ff_4_q, d_ff_3_qn, d_ff_2_qn, d_ff_1_q);
  and and_2 (and_2_out, d_ff_5_q, clock_1_out);
  D_Flip_Flop d_ff_5 (.clk(not_1_out), .D(and_1_out), .Q(d_ff_5_q));  // open: Qn, preset, en, reset
  Clock clock_1 (.out(clock_1_out));
  D_Flip_Flop d_ff_6 (.clk(clk_out), .D(d_ff_5_q), .Q(\output ));  // open: Qn, preset, en, reset
endmodule
