// Logisim project exercicio02.circ as structural Verilog: 1 circuit, main circuit main
module main (
  input  in_1,
  input  in_2,
  input  in_3,
  output out_4,
  output out_5,
  output out_6,
  output out_7,
  output out_8
);

  wire clock_1_out;

  Clock clock_1 (.out(clock_1_out));
  D_Flip_Flop d_ff_1 (.clk(clock_1_out), .D(out_5), .Q(out_4), .preset(in_3), .reset(in_2));  // open: Qn, en
  D_Flip_Flop d_ff_2 (.clk(clock_1_out), .D(out_6), .Q(out_5), .preset(in_3), .reset(in_2));  // open: Qn, en
  D_Flip_Flop d_ff_3 (.clk(clock_1_out), .D(out_7), .Q(out_6), .preset(in_3), .reset(in_2));  // open: Qn, en
  D_Flip_Flop d_ff_4 (.clk(clock_1_out), .D(out_8), .Q(out_7), .preset(in_3), .reset(in_2));  // open: Qn, en
  D_Flip_Flop d_ff_5 (.D(in_1), .Q(out_8));  // open: clk, Qn, preset, en, reset

  // Notes on the sheet:
  //   Lucas Siqueira Chagas - 380783
endmodule
