// Logisim project Exemplo0062.circ as structural Verilog: 1 circuit, main circuit main
module main (
  input  data,
  input  CLR,
  input  in_3,
  input  in_4,
  input  in_5,
  input  in_6,
  input  in_7,
  output a,
  output b,
  output c,
  output d,
  output e
);

  wire CLK_out;

  Clock CLK (.out(CLK_out));
  D_Flip_Flop d_ff_1 (.clk(CLK_out), .D(b), .Q(a), .preset(in_3), .reset(CLR));  // open: Qn, en
  D_Flip_Flop d_ff_2 (.clk(CLK_out), .D(c), .Q(b), .preset(in_4), .reset(CLR));  // open: Qn, en
  D_Flip_Flop d_ff_3 (.clk(CLK_out), .D(d), .Q(c), .preset(in_5), .reset(CLR));  // open: Qn, en
  D_Flip_Flop d_ff_4 (.clk(CLK_out), .D(e), .Q(d), .preset(in_6), .reset(CLR));  // open: Qn, en
  D_Flip_Flop d_ff_5 (.clk(CLK_out), .D(data), .Q(e), .preset(in_7), .reset(CLR));  // open: Qn, en
endmodule
