// Logisim project Exemplo0063.circ as structural Verilog: 1 circuit, main circuit main
module main (
  input  data,
  input  CLR,
  output a,
  output b,
  output c,
  output d,
  output e
);

  wire CLK_out, or_1_out;

  Clock CLK (.out(CLK_out));
  or or_1 (or_1_out, data, e);
  D_Flip_Flop d_ff_1 (.clk(CLK_out), .D(or_1_out), .Q(a), .reset(CLR));  // open: Qn, preset, en
  D_Flip_Flop d_ff_2 (.clk(CLK_out), .D(a), .Q(b), .reset(CLR));  // open: Qn, preset, en
  D_Flip_Flop d_ff_3 (.clk(CLK_out), .D(b), .Q(c), .reset(CLR));  // open: Qn, preset, en
  D_Flip_Flop d_ff_4 (.clk(CLK_out), .D(c), .Q(d), .reset(CLR));  // open: Qn, preset, en
  D_Flip_Flop d_ff_5 (.clk(CLK_out), .D(d), .Q(e), .reset(CLR));  // open: Qn, preset, en
endmodule
