// Logisim project Exemplo0065.circ as structural Verilog: 1 circuit, main circuit main
module main (
  input  CLR,
  input  LD,
  input  in_3,
  input  in_4,
  input  in_5,
  input  in_6,
  input  in_7,
  output a,
  output b,
  output c,
  output d,
  output e
);

  wire and_1_out, and_2_out, and_3_out, and_4_out, and_5_out, CLK_out;

  Clock CLK (.out(CLK_out));
  D_Flip_Flop d_ff_1 (.clk(CLK_out), .D(1'b0), .Q(a), .preset(and_1_out), .reset(CLR));  // open: Qn, en
  and and_1 (and_1_out, LD, in_3);
  D_Flip_Flop d_ff_2 (.clk(CLK_out), .D(a), .Q(b), .preset(and_2_out), .reset(CLR));  // open: Qn, en
  and and_2 (and_2_out, LD, in_4);
  D_Flip_Flop d_ff_3 (.clk(CLK_out), .D(b), .Q(c), .preset(and_3_out), .reset(CLR));  // open: Qn, en
  and and_3 (and_3_out, LD, in_5);
  D_Flip_Flop d_ff_4 (.clk(CLK_out), .D(c), .Q(d), .preset(and_4_out), .reset(CLR));  // open: Qn, en
  and and_4 (and_4_out, LD, in_6);
  D_Flip_Flop d_ff_5 (.clk(CLK_out), .D(d), .Q(e), .preset(and_5_out), .reset(CLR));  // open: Qn, en
  and and_5 (and_5_out, LD, in_7);
endmodule
