// Logisim project Exemplo0067.circ as structural Verilog: 1 circuit, main circuit main
module main (
  input  data,
  input  CLR,
  input  in_3,
  input  in_4,
  input  in_5,
  input  in_6,
  input  in_7,
  output a,
  output b,
  output c,
  output d,
  output e
);

  wire CLK_out, d_ff_5_qn, or_1_out;

  Clock CLK (.out(CLK_out));
  or or_1 (or_1_out, data, d_ff_5_qn);
  D_Flip_Flop d_ff_1 (.clk(CLK_out), .D(or_1_out), .Q(a), .preset(in_3), .reset(CLR));  // open: Qn, en
  D_Flip_Flop d_ff_2 (.clk(CLK_out), .D(a), .Q(b), .preset(in_4), .reset(CLR));  // open: Qn, en
  D_Flip_Flop d_ff_3 (.clk(CLK_out), .D(b), .Q(c), .preset(in_5), .reset(CLR));  // open: Qn, en
  D_Flip_Flop d_ff_4 (.clk(CLK_out), .D(c), .Q(d), .preset(in_6), .reset(CLR));  // open: Qn, en
  D_Flip_Flop d_ff_5 (.clk(CLK_out), .D(d), .Q(e), .Qn(d_ff_5_qn), .preset(in_7), .reset(CLR));  // open: en
endmodule
