// Logisim project Exercicio02.circ as structural Verilog: 1 circuit, main circuit main
module main (
  input  in_1,
  input  in_2,
  output out_3,
  output out_4,
  output out_5,
  output out_6,
  output out_7
);

  wire clock_1_out, or_1_out, or_2_out, or_3_out, or_4_out;

  Clock clock_1 (.out(clock_1_out));
  D_Flip_Flop d_ff_1 (.clk(clock_1_out), .D(or_1_out), .Q(out_3));  // open: Qn, preset, en, reset
  or or_1 (or_1_out, out_4, in_1);
  or or_2 (or_2_out, out_5, in_1);
  D_Flip_Flop d_ff_2 (.clk(clock_1_out), .D(or_2_out), .Q(out_4));  // open: Qn, preset, en, reset
  or or_3 (or_3_out, out_6, in_1);
  D_Flip_Flop d_ff_3 (.clk(clock_1_out), .D(or_3_out), .Q(out_5));  // open: Qn, preset, en, reset
  D_Flip_Flop d_ff_4 (.clk(clock_1_out), .D(or_4_out), .Q(out_6));  // open: Qn, preset, en, reset
  or or_4 (or_4_out, out_7, in_1);
  D_Flip_Flop d_ff_5 (.clk(clock_1_out), .D(in_1), .Q(out_7), .reset(in_2));  // open: Qn, preset, en
endmodule
