// Logisim project Exercicio05.circ as structural Verilog: 1 circuit, main circuit main
module main (
  input  CLR,
  input  LD,
  input  in_3,
  input  in_4,
  input  in_5,
  input  in_6,
  input  in_7,
  output out_8,
  output out_9,
  output out_10,
  output out_11,
  output out_12
);

  wire and_1_out, and_2_out, and_3_out, and_4_out, and_5_out, clock_1_out, undriven;

  Clock clock_1 (.out(clock_1_out));
  D_Flip_Flop d_ff_1 (.clk(clock_1_out), .D(undriven), .Q(out_8), .en(and_1_out), .reset(CLR));  // open: Qn, preset
  and and_1 (and_1_out, LD, in_3);
  D_Flip_Flop d_ff_2 (.clk(clock_1_out), .D(out_8), .Q(out_9), .en(and_2_out), .reset(CLR));  // open: Qn, preset
  and and_2 (and_2_out, LD, in_4);
  and and_3 (and_3_out, LD, in_5);
  D_Flip_Flop d_ff_3 (.clk(clock_1_out), .D(out_9), .Q(out_10), .en(and_3_out), .reset(CLR));  // open: Qn, preset
  D_Flip_Flop d_ff_4 (.clk(clock_1_out), .D(out_10), .Q(out_11), .en(and_4_out), .reset(CLR));  // open: Qn, preset
  and and_4 (and_4_out, LD, in_6);
  buf and_5 (and_5_out, in_7);  // AND_Gate
  D_Flip_Flop d_ff_5 (.clk(clock_1_out), .D(out_11), .Q(out_12), .en(and_5_out), .reset(CLR));  // open: Qn, preset
endmodule
