// Logisim project Circuitos.circ as structural Verilog
module Exercicio01 (
  input  clr,
  input  data,
  output out_3,
  output out_4,
  output out_5,
  output out_6,
  output out_7
);

  wire clk_out;

  Clock clk (.out(clk_out));
  D_Flip_Flop d_ff_1 (.clk(clk_out), .D(out_4), .Q(out_3), .reset(clr));  // open: Qn, preset, en
  D_Flip_Flop d_ff_2 (.clk(clk_out), .D(out_5), .Q(out_4), .reset(clr));  // open: Qn, preset, en
  D_Flip_Flop d_ff_3 (.clk(clk_out), .D(out_6), .Q(out_5), .reset(clr));  // open: Qn, preset, en
  D_Flip_Flop d_ff_4 (.clk(clk_out), .D(out_7), .Q(out_6), .reset(clr));  // open: Qn, preset, en
  D_Flip_Flop d_ff_5 (.clk(clk_out), .D(data), .Q(out_7), .reset(clr));  // open: Qn, preset, en
endmodule

module Exercicio02 (
  input  clr,
  input  ld,
  input  dt3,
  input  dt2,
  input  dt1,
  input  dt0,
  input  dt0_2,
  output out_8,
  output out_9,
  output out_10,
  output out_11,
  output out_12
);

  wire and_1_out, and_2_out, and_3_out, and_4_out, and_5_out, clk_out;

  Clock clk (.out(clk_out));
  and and_1 (and_1_out, dt3, ld);
  D_Flip_Flop d_ff_1 (.clk(clk_out), .D(out_9), .Q(out_8), .preset(and_1_out), .reset(clr));  // open: Qn, en
  and and_2 (and_2_out, dt2, ld);
  D_Flip_Flop d_ff_2 (.clk(clk_out), .D(out_10), .Q(out_9), .preset(and_2_out), .reset(clr));  // open: Qn, en
  and and_3 (and_3_out, dt1, ld);
  D_Flip_Flop d_ff_3 (.clk(clk_out), .D(out_11), .Q(out_10), .preset(and_3_out), .reset(clr));  // open: Qn, en
  and and_4 (and_4_out, dt0, ld);
  D_Flip_Flop d_ff_4 (.clk(clk_out), .D(out_12), .Q(out_11), .preset(and_4_out), .reset(clr));  // open: Qn, en
  and and_5 (and_5_out, dt0_2, ld);
  D_Flip_Flop d_ff_5 (.clk(clk_out), .D(1'b0), .Q(out_12), .preset(and_5_out), .reset(clr));  // open: Qn, en
endmodule

module Exercicio03 (
  input  x,
  input  clr,
  output out_3,
  output out_4,
  output out_5,
  output out_6,
  output out_7
);

  wire clk_out, or_1_out;

  Clock clk (.out(clk_out));
  or or_1 (or_1_out, x, out_7);
  D_Flip_Flop d_ff_1 (.clk(clk_out), .D(or_1_out), .Q(out_3), .reset(clr));  // open: Qn, preset, en
  D_Flip_Flop d_ff_2 (.clk(clk_out), .D(out_3), .Q(out_4), .reset(clr));  // open: Qn, preset, en
  D_Flip_Flop d_ff_3 (.clk(clk_out), .D(out_4), .Q(out_5), .reset(clr));  // open: Qn, preset, en
  D_Flip_Flop d_ff_4 (.clk(clk_out), .D(out_5), .Q(out_6), .reset(clr));  // open: Qn, preset, en
  D_Flip_Flop d_ff_5 (.clk(clk_out), .D(out_6), .Q(out_7), .reset(clr));  // open: Qn, preset, en
endmodule

module Exercicio04 (
  input  clr,
  output out_2,
  output out_3,
  output out_4,
  output out_5,
  output out_6
);

  wire clk_out, d_ff_5_qn;

  Clock clk (.out(clk_out));
  D_Flip_Flop d_ff_1 (.clk(clk_out), .D(d_ff_5_qn), .Q(out_2), .reset(clr));  // open: Qn, preset, en
  D_Flip_Flop d_ff_2 (.clk(clk_out), .D(out_2), .Q(out_3), .reset(clr));  // open: Qn, preset, en
  D_Flip_Flop d_ff_3 (.clk(clk_out), .D(out_3), .Q(out_4), .reset(clr));  // open: Qn, preset, en
  D_Flip_Flop d_ff_4 (.clk(clk_out), .D(out_4), .Q(out_5), .reset(clr));  // open: Qn, preset, en
  D_Flip_Flop d_ff_5 (.clk(clk_out), .D(out_5), .Q(out_6), .Qn(d_ff_5_qn));  // open: preset, en, reset
endmodule

module Exercicio05 (
  input  clr,
  input  ld,
  input  dt0,
  input  dt1,
  input  dt2,
  input  dt3,
  input  dt3_2,
  output out_8,
  output out_9,
  output out_10,
  output out_11,
  output out_12
);

  wire and_1_out, and_2_out, and_3_out, and_4_out, and_5_out, clk_out;

  Clock clk (.out(clk_out));
  D_Flip_Flop d_ff_1 (.clk(clk_out), .D(1'b0), .Q(out_8), .preset(and_1_out), .reset(clr));  // open: Qn, en
  and and_1 (and_1_out, dt0, ld);
  D_Flip_Flop d_ff_2 (.clk(clk_out), .D(out_8), .Q(out_9), .preset(and_2_out), .reset(clr));  // open: Qn, en
  and and_2 (and_2_out, dt1, ld);
  D_Flip_Flop d_ff_3 (.clk(clk_out), .D(out_9), .Q(out_10), .preset(and_3_out), .reset(clr));  // open: Qn, en
  and and_3 (and_3_out, dt2, ld);
  D_Flip_Flop d_ff_4 (.clk(clk_out), .D(out_10), .Q(out_11), .preset(and_4_out), .reset(clr));  // open: Qn, en
  and and_4 (and_4_out, dt3, ld);
  D_Flip_Flop d_ff_5 (.clk(clk_out), .D(out_11), .Q(out_12), .preset(and_5_out), .reset(clr));  // open: Qn, en
  and and_5 (and_5_out, dt3_2, ld);
endmodule

module Exercicio06 (
  input  clr,
  input  ld,
  input  dt0,
  input  dt1,
  input  dt2,
  input  dt3,
  input  dt3_2,
  output out_8,
  output out_9,
  output out_10,
  output out_11,
  output out_12
);

  wire and_1_out, and_2_out, and_3_out, and_4_out, and_5_out, clk_out;

  Clock clk (.out(clk_out));
  D_Flip_Flop d_ff_1 (.clk(clk_out), .D(out_12), .Q(out_8), .preset(and_1_out), .reset(clr));  // open: Qn, en
  and and_1 (and_1_out, dt0, ld);
  D_Flip_Flop d_ff_2 (.clk(clk_out), .D(out_8), .Q(out_9), .preset(and_2_out), .reset(clr));  // open: Qn, en
  and and_2 (and_2_out, dt1, ld);
  D_Flip_Flop d_ff_3 (.clk(clk_out), .D(out_9), .Q(out_10), .preset(and_3_out), .reset(clr));  // open: Qn, en
  and and_3 (and_3_out, dt2, ld);
  D_Flip_Flop d_ff_4 (.clk(clk_out), .D(out_10), .Q(out_11), .preset(and_4_out), .reset(clr));  // open: Qn, en
  and and_4 (and_4_out, dt3, ld);
  D_Flip_Flop d_ff_5 (.clk(clk_out), .D(out_11), .Q(out_12), .preset(and_5_out), .reset(clr));  // open: Qn, en
  and and_5 (and_5_out, dt3_2, ld);
endmodule

module Exercicio07 (
  input  clr,
  input  ld,
  input  dt0,
  input  dt1,
  input  dt2,
  input  dt3,
  input  dt3_2,
  output out_8,
  output out_9,
  output out_10,
  output out_11,
  output out_12
);

  wire and_1_out, and_2_out, and_3_out, and_4_out, and_5_out, clk_out, d_ff_5_qn;

  Clock clk (.out(clk_out));
  D_Flip_Flop d_ff_1 (.clk(clk_out), .D(d_ff_5_qn), .Q(out_8), .preset(and_1_out), .reset(clr));  // open: Qn, en
  and and_1 (and_1_out, dt0, ld);
  D_Flip_Flop d_ff_2 (.clk(clk_out), .D(out_8), .Q(out_9), .preset(and_2_out), .reset(clr));  // open: Qn, en
  and and_2 (and_2_out, dt1, ld);
  D_Flip_Flop d_ff_3 (.clk(clk_out), .D(out_9), .Q(out_10), .preset(and_3_out), .reset(clr));  // open: Qn, en
  and and_3 (and_3_out, dt2, ld);
  D_Flip_Flop d_ff_4 (.clk(clk_out), .D(out_10), .Q(out_11), .preset(and_4_out), .reset(clr));  // open: Qn, en
  and and_4 (and_4_out, dt3, ld);
  D_Flip_Flop d_ff_5 (.clk(clk_out), .D(out_11), .Q(out_12), .Qn(d_ff_5_qn), .preset(and_5_out));  // open: en, reset
  and and_5 (and_5_out, dt3_2, ld);
endmodule
