// Logisim project guia08.circ as structural Verilog
module _01 (
  input  in_1,
  input  in_2,
  output out_3,
  output out_4,
  output out_5,
  output out_6,
  output out_7
);

  wire clock_1_out;

  Clock clock_1 (.out(clock_1_out));
  D_Flip_Flop d_ff_1 (.clk(clock_1_out), .D(out_4), .Q(out_3), .reset(in_2));  // open: Qn, preset, en
  D_Flip_Flop d_ff_2 (.clk(clock_1_out), .D(out_5), .Q(out_4), .reset(in_2));  // open: Qn, preset, en
  D_Flip_Flop d_ff_3 (.clk(clock_1_out), .D(out_6), .Q(out_5), .reset(in_2));  // open: Qn, preset, en
  D_Flip_Flop d_ff_4 (.clk(clock_1_out), .D(out_7), .Q(out_6), .reset(in_2));  // open: Qn, preset, en
  D_Flip_Flop d_ff_5 (.clk(clock_1_out), .D(in_1), .Q(out_7), .reset(in_2));  // open: Qn, preset, en
endmodule

module _02 (
  input  in_1,
  input  in_2,
  input  in_3,
  output out_4,
  output out_5,
  output out_6,
  output out_7,
  output out_8
);

  wire clock_1_out;

  Clock clock_1 (.out(clock_1_out));
  D_Flip_Flop d_ff_1 (.clk(clock_1_out), .D(out_5), .Q(out_4), .preset(in_3), .reset(in_2));  // open: Qn, en
  D_Flip_Flop d_ff_2 (.clk(clock_1_out), .D(out_6), .Q(out_5), .preset(in_3), .reset(in_2));  // open: Qn, en
  D_Flip_Flop d_ff_3 (.clk(clock_1_out), .D(out_7), .Q(out_6), .preset(in_3), .reset(in_2));  // open: Qn, en
  D_Flip_Flop d_ff_4 (.clk(clock_1_out), .D(out_8), .Q(out_7), .preset(in_3), .reset(in_2));  // open: Qn, en
  D_Flip_Flop d_ff_5 (.clk(clock_1_out), .D(in_1), .Q(out_8), .preset(in_3), .reset(in_2));  // open: Qn, en
endmodule

module _03 (
  input  in_1,
  input  in_2,
  input  in_3,
  output out_4,
  output out_5,
  output out_6,
  output out_7,
  output out_8
);

  wire clock_1_out, or_1_out;

  Clock clock_1 (.out(clock_1_out));
  D_Flip_Flop d_ff_1 (.clk(clock_1_out), .D(or_1_out), .Q(out_4), .preset(in_3), .reset(in_2));  // open: Qn, en
  or or_1 (or_1_out, in_1, out_8);
  D_Flip_Flop d_ff_2 (.clk(clock_1_out), .D(out_4), .Q(out_5), .reset(in_2));  // open: Qn, preset, en
  D_Flip_Flop d_ff_3 (.clk(clock_1_out), .D(out_5), .Q(out_6), .reset(in_2));  // open: Qn, preset, en
  D_Flip_Flop d_ff_4 (.clk(clock_1_out), .D(out_6), .Q(out_7), .reset(in_2));  // open: Qn, preset, en
  D_Flip_Flop d_ff_5 (.clk(clock_1_out), .D(out_7), .Q(out_8), .reset(in_2));  // open: Qn, preset, en
endmodule

module _04 (
  input  in_1,
  output out_2,
  output out_3,
  output out_4,
  output out_5,
  output out_6
);

  wire clock_1_out, d_ff_1_qn;

  Clock clock_1 (.out(clock_1_out));
  D_Flip_Flop d_ff_1 (.clk(clock_1_out), .D(out_3), .Q(out_2), .Qn(d_ff_1_qn), .reset(in_1));  // open: preset, en
  D_Flip_Flop d_ff_2 (.clk(clock_1_out), .D(out_4), .Q(out_3), .reset(in_1));  // open: Qn, preset, en
  D_Flip_Flop d_ff_3 (.clk(clock_1_out), .D(out_5), .Q(out_4), .reset(in_1));  // open: Qn, preset, en
  D_Flip_Flop d_ff_4 (.clk(clock_1_out), .D(out_6), .Q(out_5), .reset(in_1));  // open: Qn, preset, en
  D_Flip_Flop d_ff_5 (.clk(clock_1_out), .D(d_ff_1_qn), .Q(out_6), .reset(in_1));  // open: Qn, preset, en
endmodule

module _05 (
  input  in_1,
  input  in_2,
  input  in_3,
  input  in_4,
  input  in_5,
  input  in_6,
  input  in_7,
  input  in_8,
  output out_9,
  output out_10,
  output out_11,
  output out_12,
  output out_13
);

  wire and_1_out, and_2_out, and_3_out, and_4_out, and_5_out, clock_1_out;

  Clock clock_1 (.out(clock_1_out));
  D_Flip_Flop d_ff_1 (.clk(clock_1_out), .D(in_1), .Q(out_9), .preset(and_1_out), .reset(in_2));  // open: Qn, en
  and and_1 (and_1_out, in_4, in_3);
  D_Flip_Flop d_ff_2 (.clk(clock_1_out), .D(out_9), .Q(out_10), .preset(and_2_out), .reset(in_2));  // open: Qn, en
  and and_2 (and_2_out, in_5, in_3);
  D_Flip_Flop d_ff_3 (.clk(clock_1_out), .D(out_10), .Q(out_11), .preset(and_3_out), .reset(in_2));  // open: Qn, en
  and and_3 (and_3_out, in_6, in_3);
  D_Flip_Flop d_ff_4 (.clk(clock_1_out), .D(out_11), .Q(out_12), .preset(and_4_out), .reset(in_2));  // open: Qn, en
  and and_4 (and_4_out, in_7, in_3);
  D_Flip_Flop d_ff_5 (.clk(clock_1_out), .D(out_12), .Q(out_13), .preset(and_5_out), .reset(in_2));  // open: Qn, en
  and and_5 (and_5_out, in_8, in_3);
endmodule
