// Logisim project circuitos.circ as structural Verilog: 5 circuits, main circuit Exercicio01
module Exercicio01 (
  input  Clock,
  input  Data,
  input  Clear,
  output a,
  output b,
  output c,
  output d,
  output e
);

  D_Flip_Flop d_ff_1 (.clk(Clock), .D(b), .Q(a), .reset(Clear));  // open: Qn, preset, en
  D_Flip_Flop d_ff_2 (.clk(Clock), .D(c), .Q(b), .reset(Clear));  // open: Qn, preset, en
  D_Flip_Flop d_ff_3 (.clk(Clock), .D(d), .Q(c), .reset(Clear));  // open: Qn, preset, en
  D_Flip_Flop d_ff_4 (.clk(Clock), .D(e), .Q(d), .reset(Clear));  // open: Qn, preset, en
  D_Flip_Flop d_ff_5 (.clk(Clock), .D(Data), .Q(e), .reset(Clear));  // open: Qn, preset, en

  // Notes on the sheet:
  //   Exercicio01 - Djonatas Tulio Rodrigues Costa - 440954
endmodule

module Exercicio02 (
  input  Clock,
  input  Data,
  input  Clear,
  output a,
  output b,
  output c,
  output d,
  output e
);

  wire or_1_out, or_2_out, or_3_out, or_4_out;

  or or_1 (or_1_out, b, Data);
  D_Flip_Flop d_ff_1 (.clk(Clock), .D(or_1_out), .Q(a), .reset(Clear));  // open: Qn, preset, en
  or or_2 (or_2_out, c, Data);
  D_Flip_Flop d_ff_2 (.clk(Clock), .D(or_2_out), .Q(b), .reset(Clear));  // open: Qn, preset, en
  or or_3 (or_3_out, d, Data);
  D_Flip_Flop d_ff_3 (.clk(Clock), .D(or_3_out), .Q(c), .reset(Clear));  // open: Qn, preset, en
  or or_4 (or_4_out, e, Data);
  D_Flip_Flop d_ff_4 (.clk(Clock), .D(or_4_out), .Q(d), .reset(Clear));  // open: Qn, preset, en
  D_Flip_Flop d_ff_5 (.clk(Clock), .D(Data), .Q(e), .reset(Clear));  // open: Qn, preset, en

  // Notes on the sheet:
  //   Exercicio02 - Djonatas Tulio Rodrigues Costa - 440954
endmodule

module Exercicio03 (
  input  Clock,
  input  Data,
  input  Clear,
  output a,
  output b,
  output c,
  output d,
  output e
);

  wire or_1_out;

  or or_1 (or_1_out, e, Data);
  D_Flip_Flop d_ff_1 (.clk(Clock), .D(or_1_out), .Q(a), .reset(Clear));  // open: Qn, preset, en
  D_Flip_Flop d_ff_2 (.clk(Clock), .D(a), .Q(b), .reset(Clear));  // open: Qn, preset, en
  D_Flip_Flop d_ff_3 (.clk(Clock), .D(b), .Q(c), .reset(Clear));  // open: Qn, preset, en
  D_Flip_Flop d_ff_4 (.clk(Clock), .D(c), .Q(d), .reset(Clear));  // open: Qn, preset, en
  D_Flip_Flop d_ff_5 (.clk(Clock), .D(d), .Q(e), .reset(Clear));  // open: Qn, preset, en

  // Notes on the sheet:
  //   Exercicio03 - Djonatas Tulio Rodrigues Costa - 440954
endmodule

module Exercicio04 (
  input  Data,
  input  Clear,
  output a,
  output b,
  output c,
  output d,
  output e
);

  wire Clock_out, or_1_out;

  Clock Clock (.out(Clock_out));
  or or_1 (or_1_out, a, Data);
  D_Flip_Flop d_ff_1 (.clk(Clock_out), .D(b), .Q(a), .reset(Clear));  // open: Qn, preset, en
  D_Flip_Flop d_ff_2 (.clk(Clock_out), .D(c), .Q(b), .reset(Clear));  // open: Qn, preset, en
  D_Flip_Flop d_ff_3 (.clk(Clock_out), .D(d), .Q(c), .reset(Clear));  // open: Qn, preset, en
  D_Flip_Flop d_ff_4 (.clk(Clock_out), .D(e), .Q(d), .reset(Clear));  // open: Qn, preset, en
  D_Flip_Flop d_ff_5 (.clk(Clock_out), .D(or_1_out), .Q(e), .reset(Clear));  // open: Qn, preset, en

  // Notes on the sheet:
  //   Exercicio04 - Djonatas Tulio Rodrigues Costa - 440954
endmodule

module Exercicio05 (
  input  Reset,
  input  Load,
  input  d4,
  input  d3,
  input  d2,
  input  d1,
  input  d0,
  output a,
  output b,
  output c,
  output d,
  output e
);

  wire and_1_out, and_2_out, and_3_out, and_4_out, and_5_out, Clock_out;

  Clock Clock (.out(Clock_out));
  and and_1 (and_1_out, Load, d4);
  D_Flip_Flop d_ff_1 (.clk(Clock_out), .D(1'b0), .Q(a), .preset(and_1_out), .reset(Reset));  // open: Qn, en
  and and_2 (and_2_out, Load, d3);
  D_Flip_Flop d_ff_2 (.clk(Clock_out), .D(a), .Q(b), .preset(and_2_out), .reset(Reset));  // open: Qn, en
  D_Flip_Flop d_ff_3 (.clk(Clock_out), .D(b), .Q(c), .preset(and_3_out), .reset(Reset));  // open: Qn, en
  and and_3 (and_3_out, Load, d2);
  D_Flip_Flop d_ff_4 (.clk(Clock_out), .D(c), .Q(d), .preset(and_4_out), .reset(Reset));  // open: Qn, en
  and and_4 (and_4_out, Load, d1);
  and and_5 (and_5_out, Load, d0);
  D_Flip_Flop d_ff_5 (.clk(Clock_out), .D(d), .Q(e), .preset(and_5_out), .reset(Reset));  // open: Qn, en

  // Notes on the sheet:
  //   Exercicio05 - Djonatas Tulio Rodrigues Costa - 440954
endmodule
