// Logisim project Exercicio04.circ as structural Verilog: 1 circuit, main circuit main
module main (
  input  in_1
);

  wire clock_1_out, d_ff_1_qn, d_ff_2_q, d_ff_3_q, d_ff_4_q, d_ff_5_q;

  Clock clock_1 (.out(clock_1_out));
  D_Flip_Flop d_ff_1 (.clk(clock_1_out), .D(d_ff_2_q), .Qn(d_ff_1_qn), .reset(in_1));  // open: Q, preset, en
  D_Flip_Flop d_ff_2 (.clk(clock_1_out), .D(d_ff_3_q), .Q(d_ff_2_q), .reset(in_1));  // open: Qn, preset, en
  D_Flip_Flop d_ff_3 (.clk(clock_1_out), .D(d_ff_4_q), .Q(d_ff_3_q), .reset(in_1));  // open: Qn, preset, en
  D_Flip_Flop d_ff_4 (.clk(clock_1_out), .D(d_ff_5_q), .Q(d_ff_4_q), .reset(in_1));  // open: Qn, preset, en
  D_Flip_Flop d_ff_5 (.clk(clock_1_out), .D(d_ff_1_qn), .Q(d_ff_5_q), .reset(in_1));  // open: Qn, preset, en
endmodule
