// Logisim project Guia08.circ as structural Verilog: 5 circuits, main circuit Exercicio01
module Exercicio01 (
  input  in_1,
  input  in_2,
  input  in_3,
  output out_4,
  output out_5,
  output out_6,
  output out_7,
  output out_8
);

  D_Flip_Flop d_ff_1 (.clk(in_1), .D(out_4), .Q(out_4), .reset(in_3));  // open: Qn, preset, en
  D_Flip_Flop d_ff_2 (.clk(in_1), .D(out_5), .Q(out_5), .reset(in_3));  // open: Qn, preset, en
  D_Flip_Flop d_ff_3 (.clk(in_1), .D(out_6), .Q(out_6), .reset(in_3));  // open: Qn, preset, en
  D_Flip_Flop d_ff_4 (.clk(in_1), .D(out_8), .Q(out_7), .reset(in_3));  // open: Qn, preset, en
  D_Flip_Flop d_ff_5 (.clk(in_1), .D(in_2), .Q(out_8), .reset(in_3));  // open: Qn, preset, en
endmodule

module Exercicio2 (
  input  in_1,
  input  in_2,
  output out_3,
  output out_4,
  output out_5,
  output out_6,
  output out_7
);

  wire clock_1_out;

  Clock clock_1 (.out(clock_1_out));
  D_Flip_Flop d_ff_1 (.clk(clock_1_out), .D(out_3), .Q(out_3), .preset(in_1), .reset(in_2));  // open: Qn, en
  D_Flip_Flop d_ff_2 (.clk(clock_1_out), .D(out_4), .Q(out_4), .preset(in_1), .reset(in_2));  // open: Qn, en
  D_Flip_Flop d_ff_3 (.clk(clock_1_out), .D(out_5), .Q(out_5), .preset(in_1), .reset(in_2));  // open: Qn, en
  D_Flip_Flop d_ff_4 (.clk(clock_1_out), .D(out_7), .Q(out_6), .preset(in_1), .reset(in_2));  // open: Qn, en
  D_Flip_Flop d_ff_5 (.clk(clock_1_out), .D(in_1), .Q(out_7), .preset(in_1), .reset(in_2));  // open: Qn, en
endmodule

module Exercicio3 (
  input  in_1,
  input  in_2,
  output out_3,
  output out_4,
  output out_5,
  output out_6,
  output out_7
);

  wire clock_1_out, or_1_out;

  Clock clock_1 (.out(clock_1_out));
  or or_1 (or_1_out, out_7, in_1);
  D_Flip_Flop d_ff_1 (.clk(clock_1_out), .D(or_1_out), .Q(out_3), .reset(in_2));  // open: Qn, preset, en
  D_Flip_Flop d_ff_2 (.clk(clock_1_out), .D(out_3), .Q(out_4), .reset(in_2));  // open: Qn, preset, en
  D_Flip_Flop d_ff_3 (.clk(clock_1_out), .D(out_4), .Q(out_5), .reset(in_2));  // open: Qn, preset, en
  D_Flip_Flop d_ff_4 (.clk(clock_1_out), .D(out_5), .Q(out_6), .reset(in_2));  // open: Qn, preset, en
  D_Flip_Flop d_ff_5 (.clk(clock_1_out), .D(out_6), .Q(out_7), .reset(in_2));  // open: Qn, preset, en
endmodule

module Exercicio4 (
  input  in_1,
  input  in_2,
  output out_3,
  output out_4,
  output out_5,
  output out_6,
  output out_7
);

  wire clock_1_out, or_1_out;

  Clock clock_1 (.out(clock_1_out));
  D_Flip_Flop d_ff_1 (.clk(clock_1_out), .D(out_4), .Q(out_3), .reset(in_2));  // open: Qn, preset, en
  or or_1 (or_1_out, out_3, in_1);
  D_Flip_Flop d_ff_2 (.clk(clock_1_out), .D(out_5), .Q(out_4), .reset(in_2));  // open: Qn, preset, en
  D_Flip_Flop d_ff_3 (.clk(clock_1_out), .D(out_6), .Q(out_5), .reset(in_2));  // open: Qn, preset, en
  D_Flip_Flop d_ff_4 (.clk(clock_1_out), .D(out_7), .Q(out_6), .reset(in_2));  // open: Qn, preset, en
  D_Flip_Flop d_ff_5 (.clk(clock_1_out), .D(or_1_out), .Q(out_7), .preset(or_1_out), .reset(in_2));  // open: Qn, en
endmodule

module Exercicio5 (
  input  in_1,
  input  in_2,
  input  in_3,
  input  in_4,
  input  in_5,
  input  in_6,
  input  in_7,
  output out_8,
  output out_9,
  output out_10,
  output out_11,
  output out_12
);

  wire and_1_out, and_2_out, and_3_out, and_4_out, and_5_out, clock_1_out;

  Clock clock_1 (.out(clock_1_out));
  and and_1 (and_1_out, in_2, in_3);
  D_Flip_Flop d_ff_1 (.clk(clock_1_out), .D(1'b0), .Q(out_8), .preset(and_1_out), .reset(in_1));  // open: Qn, en
  D_Flip_Flop d_ff_2 (.clk(clock_1_out), .D(out_8), .Q(out_9), .preset(and_2_out), .reset(in_1));  // open: Qn, en
  and and_2 (and_2_out, in_2, in_4);
  D_Flip_Flop d_ff_3 (.clk(clock_1_out), .D(out_9), .Q(out_10), .preset(and_3_out), .reset(in_1));  // open: Qn, en
  and and_3 (and_3_out, in_2, in_5);
  D_Flip_Flop d_ff_4 (.clk(clock_1_out), .D(out_10), .Q(out_11), .preset(and_4_out), .reset(in_1));  // open: Qn, en
  and and_4 (and_4_out, in_2, in_6);
  D_Flip_Flop d_ff_5 (.clk(clock_1_out), .D(out_11), .Q(out_12), .preset(and_5_out), .reset(in_1));  // open: Qn, en
  and and_5 (and_5_out, in_2, in_7);
endmodule
