// Logisim project Circ Guia08.circ as structural Verilog
module Exemplo0081 (
  input  CLK,
  input  data,
  input  CLR,
  output out_4,
  output out_5,
  output out_6,
  output out_7,
  output out_8
);

  D_Flip_Flop d_ff_1 (.clk(CLK), .D(out_5), .Q(out_4), .reset(CLR));  // open: Qn, preset, en
  D_Flip_Flop d_ff_2 (.clk(CLK), .D(out_6), .Q(out_5), .reset(CLR));  // open: Qn, preset, en
  D_Flip_Flop d_ff_3 (.clk(CLK), .D(out_7), .Q(out_6), .reset(CLR));  // open: Qn, preset, en
  D_Flip_Flop d_ff_4 (.clk(CLK), .D(out_8), .Q(out_7), .reset(CLR));  // open: Qn, preset, en
  D_Flip_Flop d_ff_5 (.clk(CLK), .D(data), .Q(out_8), .reset(CLR));  // open: Qn, preset, en
endmodule

module Exemplo0082 (
  input  CLK,
  input  data,
  input  CLR,
  output out_4,
  output out_5,
  output out_6,
  output out_7,
  output out_8
);

  wire or_1_out, or_2_out, or_3_out, or_4_out;

  or or_1 (or_1_out, out_5, data);
  D_Flip_Flop d_ff_1 (.clk(CLK), .D(or_1_out), .Q(out_4), .reset(CLR));  // open: Qn, preset, en
  D_Flip_Flop d_ff_2 (.clk(CLK), .D(or_2_out), .Q(out_5), .reset(CLR));  // open: Qn, preset, en
  or or_2 (or_2_out, out_6, data);
  or or_3 (or_3_out, out_7, data);
  D_Flip_Flop d_ff_3 (.clk(CLK), .D(or_3_out), .Q(out_6), .reset(CLR));  // open: Qn, preset, en
  or or_4 (or_4_out, out_8, data);
  D_Flip_Flop d_ff_4 (.clk(CLK), .D(or_4_out), .Q(out_7), .reset(CLR));  // open: Qn, preset, en
  D_Flip_Flop d_ff_5 (.clk(CLK), .D(data), .Q(out_8), .reset(CLR));  // open: Qn, preset, en
endmodule

module Exemplo0083 (
  input  data,
  input  CLR,
  output out_3,
  output out_4,
  output out_5,
  output out_6,
  output out_7
);

  wire clock_1_out, or_1_out;

  Clock clock_1 (.out(clock_1_out));
  or or_1 (or_1_out, out_7, data);
  D_Flip_Flop d_ff_1 (.clk(clock_1_out), .D(or_1_out), .Q(out_3), .reset(CLR));  // open: Qn, preset, en
  D_Flip_Flop d_ff_2 (.clk(clock_1_out), .D(out_3), .Q(out_4), .reset(CLR));  // open: Qn, preset, en
  D_Flip_Flop d_ff_3 (.clk(clock_1_out), .D(out_4), .Q(out_5), .reset(CLR));  // open: Qn, preset, en
  D_Flip_Flop d_ff_4 (.clk(clock_1_out), .D(out_5), .Q(out_6), .reset(CLR));  // open: Qn, preset, en
  D_Flip_Flop d_ff_5 (.clk(clock_1_out), .D(out_6), .Q(out_7), .reset(CLR));  // open: Qn, preset, en

  // Notes on the sheet:
  //   CLK
endmodule

module Exemplo0084 (
  input  data,
  input  CLR,
  output out_3,
  output out_4,
  output out_5,
  output out_6,
  output out_7
);

  wire clock_1_out, d_ff_1_qn, or_1_out;

  Clock clock_1 (.out(clock_1_out));
  or or_1 (or_1_out, d_ff_1_qn, data);
  D_Flip_Flop d_ff_1 (.clk(clock_1_out), .D(out_4), .Q(out_3), .Qn(d_ff_1_qn), .reset(CLR));  // open: preset, en
  D_Flip_Flop d_ff_2 (.clk(clock_1_out), .D(out_5), .Q(out_4), .reset(CLR));  // open: Qn, preset, en
  D_Flip_Flop d_ff_3 (.clk(clock_1_out), .D(out_6), .Q(out_5), .reset(CLR));  // open: Qn, preset, en
  D_Flip_Flop d_ff_4 (.clk(clock_1_out), .D(out_7), .Q(out_6), .reset(CLR));  // open: Qn, preset, en
  D_Flip_Flop d_ff_5 (.clk(clock_1_out), .D(or_1_out), .Q(out_7), .reset(CLR));  // open: Qn, preset, en

  // Notes on the sheet:
  //   CLK
endmodule

module Exemplo0085 (
  input  CLR,
  input  LD,
  input  D_4,
  input  D_3,
  input  D_2,
  input  D_1,
  input  D0,
  output out_8,
  output out_9,
  output out_10,
  output out_11,
  output out_12
);

  wire and_1_out, and_2_out, and_3_out, and_4_out, and_5_out, clock_1_out;

  Clock clock_1 (.out(clock_1_out));
  D_Flip_Flop d_ff_1 (.clk(clock_1_out), .D(1'b0), .Q(out_8), .preset(and_1_out), .reset(CLR));  // open: Qn, en
  and and_1 (and_1_out, LD, D_4);
  D_Flip_Flop d_ff_2 (.clk(clock_1_out), .D(out_8), .Q(out_9), .preset(and_2_out), .reset(CLR));  // open: Qn, en
  and and_2 (and_2_out, LD, D_3);
  and and_3 (and_3_out, LD, D_2);
  D_Flip_Flop d_ff_3 (.clk(clock_1_out), .D(out_9), .Q(out_10), .preset(and_3_out), .reset(CLR));  // open: Qn, en
  D_Flip_Flop d_ff_4 (.clk(clock_1_out), .D(out_10), .Q(out_11), .preset(and_4_out), .reset(CLR));  // open: Qn, en
  and and_4 (and_4_out, LD, D_1);
  and and_5 (and_5_out, LD, D0);
  D_Flip_Flop d_ff_5 (.clk(clock_1_out), .D(out_11), .Q(out_12), .preset(and_5_out), .reset(CLR));  // open: Qn, en

  // Notes on the sheet:
  //   CLK
endmodule

module Exemplo0086 (
  input  data,
  input  CLR,
  output out_3,
  output out_4,
  output out_5,
  output out_6,
  output out_7
);

  wire clock_1_out, or_1_out, or_2_out, or_3_out, or_4_out, or_5_out;

  Clock clock_1 (.out(clock_1_out));
  or or_1 (or_1_out, out_7, data);
  D_Flip_Flop d_ff_1 (.clk(clock_1_out), .D(or_1_out), .Q(out_3), .reset(CLR));  // open: Qn, preset, en
  D_Flip_Flop d_ff_2 (.clk(clock_1_out), .D(or_2_out), .Q(out_4), .reset(CLR));  // open: Qn, preset, en
  or or_2 (or_2_out, out_3, data);
  or or_3 (or_3_out, out_4, data);
  D_Flip_Flop d_ff_3 (.clk(clock_1_out), .D(or_3_out), .Q(out_5), .reset(CLR));  // open: Qn, preset, en
  or or_4 (or_4_out, out_5, data);
  D_Flip_Flop d_ff_4 (.clk(clock_1_out), .D(or_4_out), .Q(out_6), .reset(CLR));  // open: Qn, preset, en
  or or_5 (or_5_out, out_6, data);
  D_Flip_Flop d_ff_5 (.clk(clock_1_out), .D(or_5_out), .Q(out_7), .reset(CLR));  // open: Qn, preset, en

  // Notes on the sheet:
  //   CLK
endmodule

module Exemplo0087 (
  input  data,
  input  CLR,
  output out_3,
  output out_4,
  output out_5,
  output out_6,
  output out_7
);

  wire clock_1_out, d_ff_5_qn, or_1_out, or_2_out, or_3_out, or_4_out, or_5_out;

  Clock clock_1 (.out(clock_1_out));
  or or_1 (or_1_out, d_ff_5_qn, data);
  D_Flip_Flop d_ff_1 (.clk(clock_1_out), .D(or_1_out), .Q(out_3), .reset(CLR));  // open: Qn, preset, en
  D_Flip_Flop d_ff_2 (.clk(clock_1_out), .D(or_2_out), .Q(out_4), .reset(CLR));  // open: Qn, preset, en
  or or_2 (or_2_out, out_3, data);
  or or_3 (or_3_out, out_4, data);
  D_Flip_Flop d_ff_3 (.clk(clock_1_out), .D(or_3_out), .Q(out_5), .reset(CLR));  // open: Qn, preset, en
  or or_4 (or_4_out, out_5, data);
  D_Flip_Flop d_ff_4 (.clk(clock_1_out), .D(or_4_out), .Q(out_6), .reset(CLR));  // open: Qn, preset, en
  or or_5 (or_5_out, out_6, data);
  D_Flip_Flop d_ff_5 (.clk(clock_1_out), .D(or_5_out), .Q(out_7), .Qn(d_ff_5_qn), .reset(CLR));  // open: preset, en

  // Notes on the sheet:
  //   CLK
endmodule
