// Logisim project Projeto de circuito do Exemplo0057.circ as structural Verilog: 1 circuit, main circuit Exemplo0057
module Exemplo0057 (
  input  data,
  input  CLR,
  output a,
  output b,
  output c,
  output d,
  output e
);

  wire clock_1_out;

  Clock clock_1 (.out(clock_1_out));
  D_Flip_Flop FF1 (.clk(clock_1_out), .D(b), .Q(a), .reset(CLR));  // open: Qn, preset, en
  D_Flip_Flop FF2 (.clk(clock_1_out), .D(c), .Q(b), .reset(CLR));  // open: Qn, preset, en
  D_Flip_Flop FF3 (.clk(clock_1_out), .D(d), .Q(c), .reset(CLR));  // open: Qn, preset, en
  D_Flip_Flop FF4 (.clk(clock_1_out), .D(e), .Q(d), .reset(CLR));  // open: Qn, preset, en
  D_Flip_Flop FF5 (.clk(clock_1_out), .D(data), .Q(e), .reset(CLR));  // open: Qn, preset, en
endmodule
