// Logisim project Projeto de circuito do Exemplo0058.circ as structural Verilog: 1 circuit, main circuit Exemplo0058
module Exemplo0058 (
  input  data,
  input  CLR,
  output a,
  output b,
  output c,
  output d,
  output e
);

  wire AND_1_out, AND_2_out, AND_3_out, AND_4_out, clock_1_out, not_1_out;

  Clock clock_1 (.out(clock_1_out));
  D_Flip_Flop FF1 (.clk(clock_1_out), .D(AND_1_out), .Q(a), .reset(CLR));  // open: Qn, preset, en
  and AND_1 (AND_1_out, b, not_1_out);
  not not_1 (not_1_out, data);
  D_Flip_Flop FF2 (.clk(clock_1_out), .D(AND_2_out), .Q(b), .reset(CLR));  // open: Qn, preset, en
  and AND_2 (AND_2_out, c, not_1_out);
  and AND_3 (AND_3_out, d, not_1_out);
  D_Flip_Flop FF3 (.clk(clock_1_out), .D(AND_3_out), .Q(c), .reset(CLR));  // open: Qn, preset, en
  D_Flip_Flop FF4 (.clk(clock_1_out), .D(AND_4_out), .Q(d), .reset(CLR));  // open: Qn, preset, en
  and AND_4 (AND_4_out, e, not_1_out);
  D_Flip_Flop FF5 (.clk(clock_1_out), .D(data), .Q(e), .reset(CLR));  // open: Qn, preset, en

  // Notes on the sheet:
  //   s1
  //   s2
  //   s3
  //   s4
endmodule
