// Logisim project Projeto de circuito do Exemplo0059.circ as structural Verilog: 1 circuit, main circuit Exemplo0059
module Exemplo0059 (
  input  data,
  input  CLR,
  output a,
  output b,
  output c,
  output d,
  output e
);

  wire clock_1_out, or_1_out;

  Clock clock_1 (.out(clock_1_out));
  or or_1 (or_1_out, e, data);
  D_Flip_Flop FFD_1 (.clk(clock_1_out), .D(or_1_out), .Q(a), .reset(CLR));  // open: Qn, preset, en
  D_Flip_Flop FFD_2 (.clk(clock_1_out), .D(a), .Q(b), .reset(CLR));  // open: Qn, preset, en
  D_Flip_Flop FFD_3 (.clk(clock_1_out), .D(b), .Q(c), .reset(CLR));  // open: Qn, preset, en
  D_Flip_Flop FFD_4 (.clk(clock_1_out), .D(c), .Q(d), .reset(CLR));  // open: Qn, preset, en
  D_Flip_Flop FFD_5 (.clk(clock_1_out), .D(d), .Q(e), .reset(CLR));  // open: Qn, preset, en

  // Notes on the sheet:
  //   Matrícula: 448662
  //   Nome: Josemar Alves Caetano
endmodule
