// Logisim project Projeto de circuito do Exemplo0060.circ as structural Verilog: 1 circuit, main circuit Exemplo0060
module Exemplo0060 (
  input  data,
  input  CLR,
  output e,
  output d,
  output c,
  output b,
  output a
);

  wire clock_1_out, or_1_out;

  Clock clock_1 (.out(clock_1_out));
  or or_1 (or_1_out, a, data);
  D_Flip_Flop FFD_1 (.clk(clock_1_out), .D(b), .Q(a), .reset(CLR));  // open: Qn, preset, en
  D_Flip_Flop FFD_2 (.clk(clock_1_out), .D(c), .Q(b), .reset(CLR));  // open: Qn, preset, en
  D_Flip_Flop FFD_3 (.clk(clock_1_out), .D(d), .Q(c), .reset(CLR));  // open: Qn, preset, en
  D_Flip_Flop FFD_4 (.clk(clock_1_out), .D(e), .Q(d), .reset(CLR));  // open: Qn, preset, en
  D_Flip_Flop FFD_5 (.clk(clock_1_out), .D(or_1_out), .Q(e), .reset(CLR));  // open: Qn, preset, en

  // Notes on the sheet:
  //   Matrícula: 448662
  //   Nome: Josemar Alves Caetano
endmodule
