// Logisim project Projeto de circuito do Exemplo0061.circ as structural Verilog: 1 circuit, main circuit Exemplo0061
module Exemplo0061 (
  input  CLR,
  input  LD,
  input  d4,
  input  d3,
  input  d2,
  input  d1,
  input  d0,
  output a,
  output b,
  output c,
  output d,
  output e
);

  wire AND_1_out, AND_2_out, AND_3_out, AND_4_out, AND_5_out, clock_1_out;

  Clock clock_1 (.out(clock_1_out));
  D_Flip_Flop FFD_1 (.clk(clock_1_out), .D(1'b0), .Q(a), .preset(AND_1_out), .reset(CLR));  // open: Qn, en
  and AND_1 (AND_1_out, LD, d4);
  D_Flip_Flop FFD_2 (.clk(clock_1_out), .D(a), .Q(b), .preset(AND_2_out), .reset(CLR));  // open: Qn, en
  and AND_2 (AND_2_out, LD, d3);
  D_Flip_Flop FFD_3 (.clk(clock_1_out), .D(b), .Q(c), .preset(AND_3_out), .reset(CLR));  // open: Qn, en
  and AND_3 (AND_3_out, LD, d2);
  D_Flip_Flop FFD_4 (.clk(clock_1_out), .D(c), .Q(d), .preset(AND_4_out), .reset(CLR));  // open: Qn, en
  and AND_4 (AND_4_out, LD, d1);
  D_Flip_Flop FFD_5 (.clk(clock_1_out), .D(d), .Q(e), .preset(AND_5_out), .reset(CLR));  // open: Qn, en
  and AND_5 (AND_5_out, LD, d0);

  // Notes on the sheet:
  //   Matrícula: 448662
  //   Nome: Josemar Alves Caetano
endmodule
