// Logisim project Projeto de circuito do Exemplo0063.circ as structural Verilog: 1 circuit, main circuit Exemplo0063
module Exemplo0063 (
  input  data,
  input  CLR,
  output e,
  output d,
  output c,
  output b,
  output a
);

  wire AND_1_out, AND_2_out, AND_3_out, AND_4_out, clock_1_out, not_1_out, or_1_out;

  Clock clock_1 (.out(clock_1_out));
  or or_1 (or_1_out, e, data);
  D_Flip_Flop FFD_1 (.clk(clock_1_out), .D(or_1_out), .Q(a), .reset(CLR));  // open: Qn, preset, en
  not not_1 (not_1_out, data);
  and AND_1 (AND_1_out, not_1_out, a);
  D_Flip_Flop FFD_2 (.clk(clock_1_out), .D(AND_1_out), .Q(b), .reset(CLR));  // open: Qn, preset, en
  and AND_2 (AND_2_out, b, not_1_out);
  D_Flip_Flop FFD_3 (.clk(clock_1_out), .D(AND_2_out), .Q(c), .reset(CLR));  // open: Qn, preset, en
  and AND_3 (AND_3_out, c, not_1_out);
  D_Flip_Flop FFD_4 (.clk(clock_1_out), .D(AND_3_out), .Q(d), .reset(CLR));  // open: Qn, preset, en
  and AND_4 (AND_4_out, d, not_1_out);
  D_Flip_Flop FFD_5 (.clk(clock_1_out), .D(AND_4_out), .Q(e), .reset(CLR));  // open: Qn, preset, en

  // Notes on the sheet:
  //   Matrícula: 448662
  //   Nome: Josemar Alves Caetano
endmodule
