// Logisim project testeLogisim.circ as structural Verilog
module Ex_01 (
  input  data,
  input  CLR,
  output a,
  output b,
  output c,
  output d,
  output e
);

  wire clock_1_out;

  Clock clock_1 (.out(clock_1_out));
  D_Flip_Flop d_ff_1 (.clk(clock_1_out), .D(b), .Q(a), .reset(CLR));  // open: Qn, preset, en
  D_Flip_Flop d_ff_2 (.clk(clock_1_out), .D(c), .Q(b), .reset(CLR));  // open: Qn, preset, en
  D_Flip_Flop d_ff_3 (.clk(clock_1_out), .D(d), .Q(c), .reset(CLR));  // open: Qn, preset, en
  D_Flip_Flop d_ff_4 (.clk(clock_1_out), .D(e), .Q(d), .reset(CLR));  // open: Qn, preset, en
  D_Flip_Flop d_ff_5 (.clk(clock_1_out), .D(data), .Q(e), .reset(CLR));  // open: Qn, preset, en

  // Notes on the sheet:
  //   Exercicio 001 - Guia08
  //   Átila Martins Silva Júnior - 449014
  //   CLK
endmodule

module EX_02 (
  input  CLR,
  input  LD,
  input  d4,
  input  d3,
  input  d0,
  input  d2,
  input  d1,
  output a,
  output b,
  output c,
  output d,
  output e
);

  wire and_1_out, and_2_out, and_3_out, and_4_out, and_5_out, clock_1_out;

  Clock clock_1 (.out(clock_1_out));
  and and_1 (and_1_out, LD, d4);
  D_Flip_Flop d_ff_1 (.clk(clock_1_out), .D(b), .Q(a), .preset(and_1_out), .reset(CLR));  // open: Qn, en
  D_Flip_Flop d_ff_2 (.clk(clock_1_out), .D(c), .Q(b), .preset(and_2_out), .reset(CLR));  // open: Qn, en
  and and_2 (and_2_out, LD, d3);
  D_Flip_Flop d_ff_3 (.clk(clock_1_out), .D(d), .Q(c), .preset(and_3_out), .reset(CLR));  // open: Qn, en
  and and_3 (and_3_out, LD, d2);
  and and_4 (and_4_out, LD, d1);
  D_Flip_Flop d_ff_4 (.clk(clock_1_out), .D(e), .Q(d), .preset(and_4_out), .reset(CLR));  // open: Qn, en
  D_Flip_Flop d_ff_5 (.clk(clock_1_out), .D(1'b0), .Q(e), .preset(and_5_out), .reset(CLR));  // open: Qn, en
  and and_5 (and_5_out, LD, d0);

  // Notes on the sheet:
  //   Exercicio 002 - Guia08
  //   Átila Martins Silva Júnior - 449014
  //   CLK
endmodule

module EX_03 (
  input  in,
  input  CLR,
  output a,
  output b,
  output c,
  output d,
  output e
);

  wire clock_1_out, or_1_out;

  Clock clock_1 (.out(clock_1_out));
  or or_1 (or_1_out, in, e);
  D_Flip_Flop d_ff_1 (.clk(clock_1_out), .D(or_1_out), .Q(a), .reset(CLR));  // open: Qn, preset, en
  D_Flip_Flop d_ff_2 (.clk(clock_1_out), .D(a), .Q(b), .reset(CLR));  // open: Qn, preset, en
  D_Flip_Flop d_ff_3 (.clk(clock_1_out), .D(b), .Q(c), .reset(CLR));  // open: Qn, preset, en
  D_Flip_Flop d_ff_4 (.clk(clock_1_out), .D(c), .Q(d), .reset(CLR));  // open: Qn, preset, en
  D_Flip_Flop d_ff_5 (.clk(clock_1_out), .D(d), .Q(e), .reset(CLR));  // open: Qn, preset, en

  // Notes on the sheet:
  //   Exercicio 003 - Guia08
  //   Átila Martins Silva Júnior - 449014
  //   CLK
endmodule

module EX_04 (
  input  in,
  input  CLR,
  output a,
  output b,
  output c,
  output d,
  output e
);

  wire clock_1_out, or_1_out;

  Clock clock_1 (.out(clock_1_out));
  or or_1 (or_1_out, in, a);
  D_Flip_Flop d_ff_1 (.clk(clock_1_out), .D(b), .Q(a), .reset(CLR));  // open: Qn, preset, en
  D_Flip_Flop d_ff_2 (.clk(clock_1_out), .D(c), .Q(b), .reset(CLR));  // open: Qn, preset, en
  D_Flip_Flop d_ff_3 (.clk(clock_1_out), .D(d), .Q(c), .reset(CLR));  // open: Qn, preset, en
  D_Flip_Flop d_ff_4 (.clk(clock_1_out), .D(e), .Q(d), .reset(CLR));  // open: Qn, preset, en
  D_Flip_Flop d_ff_5 (.clk(clock_1_out), .D(or_1_out), .Q(e), .reset(CLR));  // open: Qn, preset, en

  // Notes on the sheet:
  //   CLK
  //   Exercicio 004 - Guia08
  //   Átila Martins Silva Júnior - 449014
endmodule

module EX_05 (
  input  CLR,
  input  LD,
  input  d4,
  input  d3,
  input  d2,
  input  d1,
  input  d0,
  output d,
  output e,
  output a,
  output b,
  output out_12
);

  wire and_1_out, and_2_out, and_3_out, and_4_out, and_5_out, clock_1_out;

  Clock clock_1 (.out(clock_1_out));
  D_Flip_Flop d_ff_1 (.clk(clock_1_out), .D(1'b0), .Q(a), .preset(and_1_out), .reset(CLR));  // open: Qn, en
  and and_1 (and_1_out, LD, d4);
  and and_2 (and_2_out, LD, d3);
  D_Flip_Flop d_ff_2 (.clk(clock_1_out), .D(a), .Q(b), .preset(and_2_out), .reset(CLR));  // open: Qn, en
  D_Flip_Flop d_ff_3 (.clk(clock_1_out), .D(b), .Q(out_12), .preset(and_3_out), .reset(CLR));  // open: Qn, en
  and and_3 (and_3_out, LD, d2);
  D_Flip_Flop d_ff_4 (.clk(clock_1_out), .D(out_12), .Q(d), .preset(and_4_out), .reset(CLR));  // open: Qn, en
  and and_4 (and_4_out, LD, d1);
  D_Flip_Flop d_ff_5 (.clk(clock_1_out), .D(d), .Q(e), .preset(and_5_out), .reset(CLR));  // open: Qn, en
  and and_5 (and_5_out, LD, d0);

  // Notes on the sheet:
  //   Exercicio 005 - Guia08
  //   Átila Martins Silva Júnior - 449014
  //   CLK
  //   c
endmodule

module EX_06 (
  input  CLR,
  input  LD,
  input  d4,
  input  d3,
  input  d2,
  input  d1,
  input  d0,
  output a,
  output b,
  output c,
  output d,
  output e
);

  wire and_1_out, and_2_out, and_3_out, and_4_out, and_5_out, clock_1_out;

  Clock clock_1 (.out(clock_1_out));
  and and_1 (and_1_out, LD, d4);
  D_Flip_Flop d_ff_1 (.clk(clock_1_out), .D(e), .Q(a), .preset(and_1_out), .reset(CLR));  // open: Qn, en
  D_Flip_Flop d_ff_2 (.clk(clock_1_out), .D(a), .Q(b), .preset(and_2_out), .reset(CLR));  // open: Qn, en
  and and_2 (and_2_out, LD, d3);
  D_Flip_Flop d_ff_3 (.clk(clock_1_out), .D(b), .Q(c), .preset(and_3_out), .reset(CLR));  // open: Qn, en
  and and_3 (and_3_out, LD, d2);
  and and_4 (and_4_out, LD, d1);
  D_Flip_Flop d_ff_4 (.clk(clock_1_out), .D(c), .Q(d), .preset(and_4_out), .reset(CLR));  // open: Qn, en
  D_Flip_Flop d_ff_5 (.clk(clock_1_out), .D(d), .Q(e), .preset(and_5_out), .reset(CLR));  // open: Qn, en
  and and_5 (and_5_out, LD, d0);

  // Notes on the sheet:
  //   Exercicio 006 - Guia08
  //   Átila Martins Silva Júnior - 449014
  //   CLK
endmodule

module EX_07 (
  input  CLR,
  input  LD,
  input  d4,
  input  d3,
  input  d2,
  input  d1,
  input  d0,
  output a,
  output b,
  output c,
  output d,
  output e
);

  wire and_1_out, and_2_out, and_3_out, and_4_out, and_5_out, clock_1_out;

  Clock clock_1 (.out(clock_1_out));
  D_Flip_Flop d_ff_1 (.clk(clock_1_out), .D(b), .Q(a), .preset(and_1_out), .reset(CLR));  // open: Qn, en
  and and_1 (and_1_out, LD, d4);
  and and_2 (and_2_out, LD, d3);
  D_Flip_Flop d_ff_2 (.clk(clock_1_out), .D(c), .Q(b), .preset(and_2_out), .reset(CLR));  // open: Qn, en
  and and_3 (and_3_out, LD, d2);
  D_Flip_Flop d_ff_3 (.clk(clock_1_out), .D(d), .Q(c), .preset(and_3_out), .reset(CLR));  // open: Qn, en
  D_Flip_Flop d_ff_4 (.clk(clock_1_out), .D(e), .Q(d), .preset(and_4_out), .reset(CLR));  // open: Qn, en
  and and_4 (and_4_out, LD, d1);
  D_Flip_Flop d_ff_5 (.clk(clock_1_out), .D(a), .Q(e), .preset(and_5_out), .reset(CLR));  // open: Qn, en
  and and_5 (and_5_out, LD, d0);

  // Notes on the sheet:
  //   CLK
  //   Exercicio 007 - Guia08
  //   Átila Martins Silva Júnior - 449014
endmodule
