// Logisim project Exercicio02.circ as structural Verilog: 1 circuit, main circuit main
module main (
  input  CLR,
  input  DATA,
  input  in_3,
  input  in_4,
  input  in_5,
  input  in_6,
  input  in_7,
  output A,
  output B,
  output C,
  output D,
  output E
);

  wire CLK_out;

  Clock CLK (.out(CLK_out));
  D_Flip_Flop d_ff_1 (.clk(CLK_out), .Q(A), .preset(in_3), .reset(CLR));  // open: D, Qn, en
  D_Flip_Flop d_ff_2 (.clk(CLK_out), .D(A), .Q(B), .preset(in_4), .reset(CLR));  // open: Qn, en
  D_Flip_Flop d_ff_3 (.clk(CLK_out), .D(B), .Q(C), .preset(in_5), .reset(CLR));  // open: Qn, en
  D_Flip_Flop d_ff_4 (.clk(CLK_out), .D(C), .Q(D), .preset(in_6), .reset(CLR));  // open: Qn, en
  D_Flip_Flop d_ff_5 (.clk(CLK_out), .D(DATA), .Q(E), .preset(in_7), .reset(CLR));  // open: Qn, en

  // Notes on the sheet:
  //   Ana Cristina - 427385
endmodule
