// Logisim project Exercicio05.circ as structural Verilog: 1 circuit, main circuit main
module main (
  input  CLR,
  input  LD,
  input  D4,
  input  D3,
  input  D2,
  input  D1,
  input  D0,
  output A,
  output B,
  output C,
  output D,
  output E
);

  wire and_1_out, and_2_out, and_3_out, and_4_out, and_5_out, CLK_out;

  Clock CLK (.out(CLK_out));
  and and_1 (and_1_out, LD, D4);
  D_Flip_Flop d_ff_1 (.clk(CLK_out), .D(1'b0), .Q(A), .preset(and_1_out), .reset(CLR));  // open: Qn, en
  D_Flip_Flop d_ff_2 (.clk(CLK_out), .D(A), .Q(B), .preset(and_2_out), .reset(CLR));  // open: Qn, en
  and and_2 (and_2_out, LD, D3);
  D_Flip_Flop d_ff_3 (.clk(CLK_out), .D(B), .Q(C), .preset(and_3_out), .reset(CLR));  // open: Qn, en
  and and_3 (and_3_out, LD, D2);
  D_Flip_Flop d_ff_4 (.clk(CLK_out), .D(C), .Q(D), .preset(and_4_out), .reset(CLR));  // open: Qn, en
  and and_4 (and_4_out, LD, D1);
  D_Flip_Flop d_ff_5 (.D(D), .Q(E), .preset(and_5_out), .reset(CLR));  // open: clk, Qn, en
  and and_5 (and_5_out, LD, D0);

  // Notes on the sheet:
  //   Ana Cristina - 427385
endmodule
