// Logisim project ed.circ as structural Verilog: 5 circuits, main circuit main
module main (
  input  data,
  input  clr,
  output s5,
  output s4,
  output s3,
  output s2,
  output s1
);

  wire clk_out;

  Clock clk (.out(clk_out));
  D_Flip_Flop d_ff_1 (.clk(clk_out), .D(s4), .Q(s5), .reset(clr));  // open: Qn, preset, en
  D_Flip_Flop d_ff_2 (.clk(clk_out), .D(s3), .Q(s4), .reset(clr));  // open: Qn, preset, en
  D_Flip_Flop d_ff_3 (.clk(clk_out), .D(s2), .Q(s3), .reset(clr));  // open: Qn, preset, en
  D_Flip_Flop d_ff_4 (.clk(clk_out), .D(s1), .Q(s2), .reset(clr));  // open: Qn, preset, en
  D_Flip_Flop d_ff_5 (.clk(clk_out), .D(data), .Q(s1), .reset(clr));  // open: Qn, preset, en

  // Notes on the sheet:
  //   Questao 1
  //   451580
  //   Isabel Bicalho Amaro
endmodule

module q2 (
  input  data,
  input  clr,
  output out_3,
  output out_4,
  output out_5,
  output out_6,
  output out_7
);

  wire clk_out, d_ff_2_q, d_ff_3_q, d_ff_4_q, d_ff_5_q;

  Clock clk (.out(clk_out));
  D_Flip_Flop d_ff_1 (.clk(clk_out), .D(d_ff_2_q), .Qn(out_3), .reset(clr));  // open: Q, preset, en
  D_Flip_Flop d_ff_2 (.clk(clk_out), .D(d_ff_3_q), .Q(d_ff_2_q), .Qn(out_4), .reset(clr));  // open: preset, en
  D_Flip_Flop d_ff_3 (.clk(clk_out), .D(d_ff_4_q), .Q(d_ff_3_q), .Qn(out_5), .reset(clr));  // open: preset, en
  D_Flip_Flop d_ff_4 (.clk(clk_out), .D(d_ff_5_q), .Q(d_ff_4_q), .Qn(out_6), .reset(clr));  // open: preset, en
  D_Flip_Flop d_ff_5 (.clk(clk_out), .D(data), .Q(d_ff_5_q), .Qn(out_7), .reset(clr));  // open: preset, en

  // Notes on the sheet:
  //   Questao 2
  //   451580
  //   Isabel Bicalho Amaro
endmodule

module q3 (
  input  data,
  input  clr,
  output out_3,
  output out_4,
  output out_5,
  output out_6,
  output out_7
);

  wire clk_out, or_1_out;

  Clock clk (.out(clk_out));
  or or_1 (or_1_out, out_3, data);
  D_Flip_Flop d_ff_1 (.clk(clk_out), .D(out_4), .Q(out_3), .reset(clr));  // open: Qn, preset, en
  D_Flip_Flop d_ff_2 (.clk(clk_out), .D(out_5), .Q(out_4), .reset(clr));  // open: Qn, preset, en
  D_Flip_Flop d_ff_3 (.clk(clk_out), .D(out_6), .Q(out_5), .reset(clr));  // open: Qn, preset, en
  D_Flip_Flop d_ff_4 (.clk(clk_out), .D(out_7), .Q(out_6), .reset(clr));  // open: Qn, preset, en
  D_Flip_Flop d_ff_5 (.clk(clk_out), .D(or_1_out), .Q(out_7), .reset(clr));  // open: Qn, preset, en

  // Notes on the sheet:
  //   Questao 3
  //   451580
  //   Isabel Bicalho Amaro
endmodule

module q4 (
  input  data,
  output out_2,
  output out_3,
  output out_4,
  output out_5,
  output out_6
);

  wire clock_1_out, d_ff_1_qn, or_1_out;

  Clock clock_1 (.out(clock_1_out));
  D_Flip_Flop d_ff_1 (.clk(clock_1_out), .D(out_3), .Q(out_2), .Qn(d_ff_1_qn));  // open: preset, en, reset
  D_Flip_Flop d_ff_2 (.D(out_4), .Q(out_3));  // open: clk, Qn, preset, en, reset
  D_Flip_Flop d_ff_3 (.clk(clock_1_out), .D(out_5), .Q(out_4));  // open: Qn, preset, en, reset
  D_Flip_Flop d_ff_4 (.clk(clock_1_out), .D(out_6), .Q(out_5));  // open: Qn, preset, en, reset
  D_Flip_Flop d_ff_5 (.clk(clock_1_out), .D(or_1_out), .Q(out_6));  // open: Qn, preset, en, reset
  or or_1 (or_1_out, data, d_ff_1_qn);

  // Notes on the sheet:
  //   Questao 4
  //   451580
  //   Isabel Bicalho Amaro
endmodule

module q5 (
  input  clear,
  input  load,
  input  in_3,
  input  in_4,
  input  in_5,
  input  in_6,
  input  in_7,
  output out_8
);

  wire and_1_out, and_2_out, and_3_out, and_4_out, and_5_out, clock_1_out, d_ff_1_q, d_ff_2_q, d_ff_3_q,
       d_ff_4_q;

  Clock clock_1 (.out(clock_1_out));
  D_Flip_Flop d_ff_1 (.clk(clock_1_out), .D(1'b0), .Q(d_ff_1_q), .preset(and_1_out), .reset(clear));  // open: Qn, en
  and and_1 (and_1_out, load, in_3);
  and and_2 (and_2_out, load, in_4);
  D_Flip_Flop d_ff_2 (
    .clk(clock_1_out), .D(d_ff_1_q), .Q(d_ff_2_q), .preset(and_2_out), .reset(clear));  // open: Qn, en
  D_Flip_Flop d_ff_3 (
    .clk(clock_1_out), .D(d_ff_2_q), .Q(d_ff_3_q), .preset(and_3_out), .reset(clear));  // open: Qn, en
  and and_3 (and_3_out, load, in_5);
  D_Flip_Flop d_ff_4 (
    .clk(clock_1_out), .D(d_ff_3_q), .Q(d_ff_4_q), .preset(and_4_out), .reset(clear));  // open: Qn, en
  and and_4 (and_4_out, load, in_6);
  D_Flip_Flop d_ff_5 (.clk(clock_1_out), .D(d_ff_4_q), .Q(out_8), .preset(and_5_out));  // open: Qn, en, reset
  and and_5 (and_5_out, load, in_7);

  // Notes on the sheet:
  //   Questao 5
  //   Isabel Bicalho Amaro
endmodule
