// Logisim project exercicio06.circ as structural Verilog: 1 circuit, main circuit main
module main (
  input  in_1,
  input  in_2,
  output out_3,
  output out_4,
  output out_5,
  output out_6,
  output out_7
);

  wire clock_1_out, xor_1_out;

  Clock clock_1 (.out(clock_1_out));
  xor xor_1 (xor_1_out, out_7, in_1);
  D_Flip_Flop d_ff_1 (.clk(clock_1_out), .D(xor_1_out), .Q(out_3), .preset(in_2));  // open: Qn, en, reset
  D_Flip_Flop d_ff_2 (.clk(clock_1_out), .D(out_3), .Q(out_4), .preset(in_2));  // open: Qn, en, reset
  D_Flip_Flop d_ff_3 (.clk(clock_1_out), .D(out_4), .Q(out_5), .preset(in_2));  // open: Qn, en, reset
  D_Flip_Flop d_ff_4 (.clk(clock_1_out), .D(out_5), .Q(out_6), .preset(in_2));  // open: Qn, en, reset
  D_Flip_Flop d_ff_5 (.clk(clock_1_out), .D(out_6), .Q(out_7), .preset(in_2));  // open: Qn, en, reset

  // Notes on the sheet:
  //   Rodolfo Herman - 451612
endmodule
