// Logisim project EstudoDirigido08.circ as structural Verilog: 7 circuits, main circuit Exercicio01
module Exercicio01 (
  input  Load,
  input  Entrada,
  output S4,
  output S3,
  output S2,
  output S1,
  output S0
);

  wire and_1_out, Clock_out;

  Clock Clock (.out(Clock_out));
  D_Flip_Flop d_ff_1 (.clk(Clock_out), .D(S3), .Q(S4));  // open: Qn, preset, en, reset
  D_Flip_Flop d_ff_2 (.clk(Clock_out), .D(S2), .Q(S3));  // open: Qn, preset, en, reset
  D_Flip_Flop d_ff_3 (.clk(Clock_out), .D(S1), .Q(S2));  // open: Qn, preset, en, reset
  and and_1 (and_1_out, Load, Entrada);
  D_Flip_Flop d_ff_4 (.clk(Clock_out), .D(S0), .Q(S1));  // open: Qn, preset, en, reset
  D_Flip_Flop d_ff_5 (.clk(Clock_out), .D(and_1_out), .Q(S0));  // open: Qn, preset, en, reset
endmodule

module Exercicio02 (
  input  E4,
  input  E3,
  input  E2,
  input  E1,
  input  E0,
  input  Load,
  output S4,
  output S3,
  output S2,
  output S1,
  output S0
);

  wire and_1_out, and_2_out, and_3_out, and_4_out, and_5_out, Clock_out, or_1_out, or_2_out, or_3_out,
       or_4_out;

  Clock Clock (.out(Clock_out));
  and and_1 (and_1_out, Load, E4);
  or or_1 (or_1_out, and_1_out, S3);
  D_Flip_Flop d_ff_1 (.clk(Clock_out), .D(or_1_out), .Q(S4));  // open: Qn, preset, en, reset
  and and_2 (and_2_out, Load, E3);
  or or_2 (or_2_out, and_2_out, S2);
  and and_3 (and_3_out, Load, E2);
  D_Flip_Flop d_ff_2 (.clk(Clock_out), .D(or_2_out), .Q(S3));  // open: Qn, preset, en, reset
  D_Flip_Flop d_ff_3 (.clk(Clock_out), .D(or_3_out), .Q(S2));  // open: Qn, preset, en, reset
  or or_3 (or_3_out, and_3_out, S1);
  and and_4 (and_4_out, Load, E1);
  D_Flip_Flop d_ff_4 (.clk(Clock_out), .D(or_4_out), .Q(S1));  // open: Qn, preset, en, reset
  or or_4 (or_4_out, and_4_out, S0);
  and and_5 (and_5_out, Load, E0);
  D_Flip_Flop d_ff_5 (.clk(Clock_out), .D(and_5_out), .Q(S0));  // open: Qn, preset, en, reset
endmodule

module Exercicio03 (
  input  Entrada,
  input  Load,
  input  Clear,
  output S4,
  output S3,
  output S2,
  output S1,
  output S0
);

  wire and_1_out, Clock_out, d_ff_5_q;

  Clock Clock (.out(Clock_out));
  and and_1 (and_1_out, Entrada, Load);
  D_Flip_Flop d_ff_1 (.clk(Clock_out), .D(S4), .Q(S3), .reset(Clear));  // open: Qn, preset, en
  or or_1 (S4, and_1_out, d_ff_5_q);
  D_Flip_Flop d_ff_2 (.clk(Clock_out), .D(S3), .Q(S2), .reset(Clear));  // open: Qn, preset, en
  D_Flip_Flop d_ff_3 (.clk(Clock_out), .D(S2), .Q(S1), .reset(Clear));  // open: Qn, preset, en
  D_Flip_Flop d_ff_4 (.clk(Clock_out), .D(S1), .Q(S0), .reset(Clear));  // open: Qn, preset, en
  D_Flip_Flop d_ff_5 (.clk(Clock_out), .D(S0), .Q(d_ff_5_q), .reset(Clear));  // open: Qn, preset, en
endmodule

module Exercicio04 (
  input  Entrada
);

  wire Clock_out, d_ff_1_qn, d_ff_2_q, d_ff_3_q, d_ff_4_q, d_ff_5_q, or_1_out;

  Clock Clock (.out(Clock_out));
  D_Flip_Flop d_ff_1 (.clk(Clock_out), .D(d_ff_2_q), .Qn(d_ff_1_qn));  // open: Q, preset, en, reset
  D_Flip_Flop d_ff_2 (.clk(Clock_out), .D(d_ff_3_q), .Q(d_ff_2_q));  // open: Qn, preset, en, reset
  D_Flip_Flop d_ff_3 (.clk(Clock_out), .D(d_ff_4_q), .Q(d_ff_3_q));  // open: Qn, preset, en, reset
  D_Flip_Flop d_ff_4 (.clk(Clock_out), .D(d_ff_5_q), .Q(d_ff_4_q));  // open: Qn, preset, en, reset
  or or_1 (or_1_out, Entrada, d_ff_1_qn);
  D_Flip_Flop d_ff_5 (.clk(Clock_out), .D(or_1_out), .Q(d_ff_5_q));  // open: Qn, preset, en, reset
endmodule

module Exercicio05 (
  input  Clear,
  input  load,
  input  b4,
  input  b3,
  input  b2,
  input  b1,
  input  b0,
  output Saida_Serial
);

  wire and_1_out, and_2_out, and_3_out, and_4_out, and_5_out, clock_1_out, d_ff_1_q, d_ff_2_q, d_ff_3_q,
       d_ff_4_q;

  Clock clock_1 (.out(clock_1_out));
  D_Flip_Flop d_ff_1 (.clk(clock_1_out), .D(1'b0), .Q(d_ff_1_q), .preset(and_1_out), .reset(Clear));  // open: Qn, en
  and and_1 (and_1_out, load, b4);
  D_Flip_Flop d_ff_2 (
    .clk(clock_1_out), .D(d_ff_1_q), .Q(d_ff_2_q), .preset(and_2_out), .reset(Clear));  // open: Qn, en
  and and_2 (and_2_out, load, b3);
  D_Flip_Flop d_ff_3 (
    .clk(clock_1_out), .D(d_ff_2_q), .Q(d_ff_3_q), .preset(and_3_out), .reset(Clear));  // open: Qn, en
  and and_3 (and_3_out, load, b2);
  and and_4 (and_4_out, load, b1);
  D_Flip_Flop d_ff_4 (
    .clk(clock_1_out), .D(d_ff_3_q), .Q(d_ff_4_q), .preset(and_4_out), .reset(Clear));  // open: Qn, en
  and and_5 (and_5_out, load, b0);
  D_Flip_Flop d_ff_5 (
    .clk(clock_1_out), .D(d_ff_4_q), .Q(Saida_Serial), .preset(and_5_out), .reset(Clear));  // open: Qn, en

  // Notes on the sheet:
  //   Entrada Paralela
endmodule

module Exercicio06 (
  input  Clear,
  input  Load,
  input  E4,
  input  E3,
  input  E2,
  input  E1,
  input  E0,
  output S4,
  output S3,
  output S2,
  output S1,
  output S0
);

  wire and_1_out, and_2_out, and_3_out, and_4_out, and_5_out, Clock_out, or_1_out, or_2_out, or_3_out,
       or_4_out, or_5_out;

  Clock Clock (.out(Clock_out));
  or or_1 (or_1_out, and_1_out, S0);
  and and_1 (and_1_out, Load, E4);
  D_Flip_Flop d_ff_1 (.clk(Clock_out), .D(or_1_out), .Q(S4), .reset(Clear));  // open: Qn, preset, en
  and and_2 (and_2_out, Load, E3);
  D_Flip_Flop d_ff_2 (.clk(Clock_out), .D(or_2_out), .Q(S3), .reset(Clear));  // open: Qn, preset, en
  or or_2 (or_2_out, S4, and_2_out);
  or or_3 (or_3_out, S3, and_3_out);
  and and_3 (and_3_out, Load, E2);
  D_Flip_Flop d_ff_3 (.clk(Clock_out), .D(or_3_out), .Q(S2), .reset(Clear));  // open: Qn, preset, en
  or or_4 (or_4_out, S2, and_4_out);
  and and_4 (and_4_out, Load, E1);
  D_Flip_Flop d_ff_4 (.clk(Clock_out), .D(or_4_out), .Q(S1), .reset(Clear));  // open: Qn, preset, en
  or or_5 (or_5_out, S1, and_5_out);
  and and_5 (and_5_out, Load, E0);
  D_Flip_Flop d_ff_5 (.clk(Clock_out), .D(or_5_out), .Q(S0), .reset(Clear));  // open: Qn, preset, en
endmodule

module Exercicio07 (
  input  Clear,
  input  Load,
  input  E4,
  input  E3,
  input  E2,
  input  E1,
  input  E0,
  output S4,
  output S3,
  output S2,
  output S1,
  output S0
);

  wire and_1_out, and_2_out, and_3_out, and_4_out, and_5_out, Clock_out, d_ff_5_qn, or_1_out, or_2_out,
       or_3_out, or_4_out, or_5_out;

  Clock Clock (.out(Clock_out));
  or or_1 (or_1_out, and_1_out, d_ff_5_qn);
  and and_1 (and_1_out, Load, E4);
  D_Flip_Flop d_ff_1 (.clk(Clock_out), .D(or_1_out), .Q(S4), .reset(Clear));  // open: Qn, preset, en
  and and_2 (and_2_out, Load, E3);
  D_Flip_Flop d_ff_2 (.clk(Clock_out), .D(or_2_out), .Q(S3), .reset(Clear));  // open: Qn, preset, en
  or or_2 (or_2_out, S4, and_2_out);
  or or_3 (or_3_out, S3, and_3_out);
  and and_3 (and_3_out, Load, E2);
  D_Flip_Flop d_ff_3 (.clk(Clock_out), .D(or_3_out), .Q(S2), .reset(Clear));  // open: Qn, preset, en
  or or_4 (or_4_out, S2, and_4_out);
  and and_4 (and_4_out, Load, E1);
  D_Flip_Flop d_ff_4 (.clk(Clock_out), .D(or_4_out), .Q(S1), .reset(Clear));  // open: Qn, preset, en
  or or_5 (or_5_out, S1, and_5_out);
  and and_5 (and_5_out, Load, E0);
  D_Flip_Flop d_ff_5 (.clk(Clock_out), .D(or_5_out), .Q(S0), .Qn(d_ff_5_qn), .reset(Clear));  // open: preset, en
endmodule
