// Logisim project Exercicio02.circ as structural Verilog: 1 circuit, main circuit main
module main (
  input  Entrada,
  input  CLR,
  output out_3,
  output out_4,
  output out_5,
  output out_6,
  output out_7
);

  wire CLK_out, d_ff_2_q, d_ff_3_q, d_ff_4_q, d_ff_5_q;

  Clock CLK (.out(CLK_out));
  D_Flip_Flop d_ff_1 (.clk(CLK_out), .D(d_ff_2_q), .Qn(out_3), .reset(CLR));  // open: Q, preset, en
  D_Flip_Flop d_ff_2 (.clk(CLK_out), .D(d_ff_3_q), .Q(d_ff_2_q), .Qn(out_4), .reset(CLR));  // open: preset, en
  D_Flip_Flop d_ff_3 (.clk(CLK_out), .D(d_ff_4_q), .Q(d_ff_3_q), .Qn(out_5), .reset(CLR));  // open: preset, en
  D_Flip_Flop d_ff_4 (.clk(CLK_out), .D(d_ff_5_q), .Q(d_ff_4_q), .Qn(out_6), .reset(CLR));  // open: preset, en
  D_Flip_Flop d_ff_5 (.clk(CLK_out), .D(Entrada), .Q(d_ff_5_q), .Qn(out_7), .reset(CLR));  // open: preset, en
endmodule
