// Logisim project Exercicio04.circ as structural Verilog: 1 circuit, main circuit main
module main (
  input  in_1,
  output out_2,
  output out_3,
  output out_4,
  output out_5,
  output out_6
);

  wire clock_1_out, j_k_ff_1_qn, j_k_ff_2_qn, j_k_ff_3_qn, j_k_ff_4_qn, j_k_ff_5_qn;

  Clock clock_1 (.out(clock_1_out));
  J_K_Flip_Flop j_k_ff_1 (
    .J(out_3), .clk(clock_1_out), .K(j_k_ff_2_qn), .Q(out_2), .Qn(j_k_ff_1_qn), .reset(in_1));  // open: preset, en
  J_K_Flip_Flop j_k_ff_2 (
    .J(out_4), .clk(clock_1_out), .K(j_k_ff_3_qn), .Q(out_3), .Qn(j_k_ff_2_qn), .reset(in_1));  // open: preset, en
  J_K_Flip_Flop j_k_ff_3 (
    .J(out_5), .clk(clock_1_out), .K(j_k_ff_4_qn), .Q(out_4), .Qn(j_k_ff_3_qn), .reset(in_1));  // open: preset, en
  J_K_Flip_Flop j_k_ff_4 (
    .J(out_6), .clk(clock_1_out), .K(j_k_ff_5_qn), .Q(out_5), .Qn(j_k_ff_4_qn), .reset(in_1));  // open: preset, en
  J_K_Flip_Flop j_k_ff_5 (
    .J(j_k_ff_1_qn), .clk(clock_1_out), .K(out_2), .Q(out_6), .Qn(j_k_ff_5_qn), .reset(in_1));  // open: preset, en
endmodule
