// Logisim project Exercicio02.circ as structural Verilog: 1 circuit, main circuit main
module main (
  input  Data,
  input  Clear,
  output out_3,
  output out_4,
  output out_5,
  output out_6,
  output out_7
);

  wire Clk_out;

  Clock Clk (.out(Clk_out));
  D_Flip_Flop d_ff_1 (.clk(Clk_out), .D(out_4), .Q(out_3), .preset(Data), .reset(Clear));  // open: Qn, en
  D_Flip_Flop d_ff_2 (.clk(Clk_out), .D(out_5), .Q(out_4), .preset(Data), .reset(Clear));  // open: Qn, en
  D_Flip_Flop d_ff_3 (.clk(Clk_out), .D(out_6), .Q(out_5), .preset(Data), .reset(Clear));  // open: Qn, en
  D_Flip_Flop d_ff_4 (.clk(Clk_out), .D(out_7), .Q(out_6), .preset(Data), .reset(Clear));  // open: Qn, en
  D_Flip_Flop d_ff_5 (.clk(Clk_out), .D(Data), .Q(out_7), .preset(Data), .reset(Clear));  // open: Qn, en

  // Notes on the sheet:
  //   462017
  //   Breno Macena Pereira de Souza
endmodule
