// Logisim project Exercicio05.circ as structural Verilog: 1 circuit, main circuit main
module main (
  input  Clear,
  input  LD,
  input  in_3,
  input  in_4,
  input  in_5,
  input  in_6,
  input  in_7,
  output out_8,
  output out_9,
  output out_10,
  output out_11,
  output out_12
);

  wire and_1_out, and_2_out, and_3_out, and_4_out, and_5_out, Clk_out;

  Clock Clk (.out(Clk_out));
  D_Flip_Flop d_ff_1 (.clk(Clk_out), .D(1'b0), .Q(out_8), .preset(and_1_out), .reset(Clear));  // open: Qn, en
  and and_1 (and_1_out, LD, in_3);
  D_Flip_Flop d_ff_2 (.clk(Clk_out), .D(out_8), .Q(out_9), .preset(and_2_out), .reset(Clear));  // open: Qn, en
  and and_2 (and_2_out, LD, in_4);
  D_Flip_Flop d_ff_3 (.clk(Clk_out), .D(out_9), .Q(out_10), .preset(and_3_out), .reset(Clear));  // open: Qn, en
  and and_3 (and_3_out, LD, in_5);
  D_Flip_Flop d_ff_4 (.clk(Clk_out), .D(out_10), .Q(out_11), .preset(and_4_out), .reset(Clear));  // open: Qn, en
  and and_4 (and_4_out, LD, in_6);
  D_Flip_Flop d_ff_5 (.clk(Clk_out), .D(out_11), .Q(out_12), .preset(and_5_out), .reset(Clear));  // open: Qn, en
  and and_5 (and_5_out, LD, in_7);

  // Notes on the sheet:
  //   462017
  //   Breno Macena Pereira de Souza
endmodule
