// Logisim project exercicio07.circ as structural Verilog: 1 circuit, main circuit main
module main (
  input  data,
  input  Clear,
  output out_3,
  output out_4,
  output out_5,
  output out_6,
  output out_7
);

  wire Clk_out, d_ff_5_qn, or_1_out;

  Clock Clk (.out(Clk_out));
  D_Flip_Flop d_ff_1 (.clk(Clk_out), .D(or_1_out), .Q(out_3), .preset(data), .reset(Clear));  // open: Qn, en
  or or_1 (or_1_out, data, d_ff_5_qn);
  D_Flip_Flop d_ff_2 (.clk(Clk_out), .D(out_3), .Q(out_4), .preset(data), .reset(Clear));  // open: Qn, en
  D_Flip_Flop d_ff_3 (.clk(Clk_out), .D(out_4), .Q(out_5), .preset(data), .reset(Clear));  // open: Qn, en
  D_Flip_Flop d_ff_4 (.clk(Clk_out), .D(out_5), .Q(out_6), .preset(data), .reset(Clear));  // open: Qn, en
  D_Flip_Flop d_ff_5 (.clk(Clk_out), .D(out_6), .Q(out_7), .Qn(d_ff_5_qn), .preset(data), .reset(Clear));  // open: en

  // Notes on the sheet:
  //   462017
  //   Breno Macena Pereira de Souza
endmodule
