// Logisim project Exercicio03 -.circ as structural Verilog: 1 circuit, main circuit main
module main (
  input  _1,
  output A,
  output B,
  output C,
  output D,
  output E,
  output F
);

  wire and_1_out, and_2_out, j_k_ff_2_qn, j_k_ff_4_qn, j_k_ff_6_qn, not_1_out, not_2_out, or_1_out, PULSE_out;

  Clock PULSE (.out(PULSE_out));
  not not_1 (not_1_out, _1);
  J_K_Flip_Flop j_k_ff_1 (.J(_1), .clk(PULSE_out), .K(_1), .Q(F), .preset(or_1_out));  // open: Qn, en, reset
  or or_1 (or_1_out, not_1_out, and_2_out, and_1_out);
  and and_1 (and_1_out, F, j_k_ff_2_qn, D, B, j_k_ff_6_qn);
  and and_2 (and_2_out, j_k_ff_2_qn, not_2_out);
  not not_2 (not_2_out, C);
  J_K_Flip_Flop j_k_ff_2 (.J(_1), .clk(F), .K(_1), .Q(E), .Qn(j_k_ff_2_qn), .preset(or_1_out));  // open: en, reset
  J_K_Flip_Flop j_k_ff_3 (.J(_1), .clk(E), .K(_1), .Q(D), .preset(or_1_out));  // open: Qn, en, reset
  J_K_Flip_Flop j_k_ff_4 (.J(_1), .clk(D), .K(_1), .Q(C), .Qn(j_k_ff_4_qn), .preset(or_1_out));  // open: en, reset
  J_K_Flip_Flop j_k_ff_5 (.J(_1), .clk(C), .K(_1), .Q(B), .preset(or_1_out));  // open: Qn, en, reset
  // Probe on {A, B, C, D, E, F}
  J_K_Flip_Flop j_k_ff_6 (.J(_1), .clk(B), .K(_1), .Q(A), .Qn(j_k_ff_6_qn), .preset(or_1_out));  // open: en, reset
endmodule
