// Logisim project Exercicio04.circ as structural Verilog: 1 circuit, main circuit main
module main (
  input  _1,
  input  CLR,
  output A,
  output B,
  output C,
  output D,
  output E,
  output F
);

  wire j_k_ff_1_qn, j_k_ff_2_qn, j_k_ff_3_qn, j_k_ff_4_qn, j_k_ff_5_qn, j_k_ff_6_qn, nand_1_out, nand_2_out,
       PULSE_out;

  Clock PULSE (.out(PULSE_out));
  nand nand_1 (nand_1_out, j_k_ff_1_qn, E, C, j_k_ff_5_qn, j_k_ff_6_qn);
  J_K_Flip_Flop j_k_ff_1 (
    .J(_1), .clk(PULSE_out), .K(_1), .Q(F), .Qn(j_k_ff_1_qn), .reset(nand_2_out));  // open: preset, en
  nand nand_2 (nand_2_out, CLR, nand_1_out);
  J_K_Flip_Flop j_k_ff_2 (
    .J(_1), .clk(j_k_ff_1_qn), .K(_1), .Q(E), .Qn(j_k_ff_2_qn), .reset(nand_2_out));  // open: preset, en
  J_K_Flip_Flop j_k_ff_3 (
    .J(_1), .clk(j_k_ff_2_qn), .K(_1), .Q(D), .Qn(j_k_ff_3_qn), .reset(nand_2_out));  // open: preset, en
  J_K_Flip_Flop j_k_ff_4 (
    .J(_1), .clk(j_k_ff_3_qn), .K(_1), .Q(C), .Qn(j_k_ff_4_qn), .reset(nand_2_out));  // open: preset, en
  J_K_Flip_Flop j_k_ff_5 (
    .J(_1), .clk(j_k_ff_4_qn), .K(_1), .Q(B), .Qn(j_k_ff_5_qn), .reset(nand_2_out));  // open: preset, en
  J_K_Flip_Flop j_k_ff_6 (
    .J(_1), .clk(j_k_ff_5_qn), .K(_1), .Q(A), .Qn(j_k_ff_6_qn), .reset(nand_2_out));  // open: preset, en
endmodule
