// Logisim project Exercicio05.circ as structural Verilog: 1 circuit, main circuit main
module main (
  input  CLR,
  output D,
  output C,
  output B,
  output A
);

  wire and_1_out, or_1_out, PULSE_out, t_ff_2_qn, t_ff_3_qn, t_ff_4_qn;

  Clock PULSE (.out(PULSE_out));
  or or_1 (or_1_out, CLR, and_1_out);
  and and_1 (and_1_out, D, B, t_ff_4_qn);
  T_Flip_Flop t_ff_1 (.clk(t_ff_2_qn), .T(t_ff_2_qn), .Q(D), .reset(or_1_out));  // open: Qn, preset, en
  T_Flip_Flop t_ff_2 (.clk(t_ff_3_qn), .T(t_ff_3_qn), .Q(C), .Qn(t_ff_2_qn), .reset(or_1_out));  // open: preset, en
  T_Flip_Flop t_ff_3 (.clk(t_ff_4_qn), .T(t_ff_4_qn), .Q(B), .Qn(t_ff_3_qn), .reset(or_1_out));  // open: preset, en
  T_Flip_Flop t_ff_4 (.clk(PULSE_out), .T(PULSE_out), .Q(A), .Qn(t_ff_4_qn), .reset(or_1_out));  // open: preset, en
endmodule
