// Logisim project Extras02.circ as structural Verilog: 1 circuit, main circuit main
module main (
  input  INPUT,
  input  CLR,
  output A,
  output B,
  output C,
  output D,
  output E,
  output F
);

  wire CLK_out, j_k_ff_1_qn, j_k_ff_2_qn, j_k_ff_3_qn, j_k_ff_4_qn, j_k_ff_5_qn, j_k_ff_6_qn, not_1_out,
       not_2_out, or_1_out;

  Clock CLK (.out(CLK_out));
  not not_1 (not_1_out, or_1_out);
  or or_1 (or_1_out, INPUT, not_2_out);
  not not_2 (not_2_out, j_k_ff_6_qn);
  J_K_Flip_Flop j_k_ff_1 (
    .J(or_1_out), .clk(CLK_out), .K(not_1_out), .Q(A), .Qn(j_k_ff_1_qn), .reset(CLR));  // open: preset, en
  J_K_Flip_Flop j_k_ff_2 (
    .J(A), .clk(CLK_out), .K(j_k_ff_1_qn), .Q(B), .Qn(j_k_ff_2_qn), .reset(CLR));  // open: preset, en
  J_K_Flip_Flop j_k_ff_3 (
    .J(B), .clk(CLK_out), .K(j_k_ff_2_qn), .Q(C), .Qn(j_k_ff_3_qn), .reset(CLR));  // open: preset, en
  J_K_Flip_Flop j_k_ff_4 (
    .J(C), .clk(CLK_out), .K(j_k_ff_3_qn), .Q(D), .Qn(j_k_ff_4_qn), .reset(CLR));  // open: preset, en
  J_K_Flip_Flop j_k_ff_5 (
    .J(D), .clk(CLK_out), .K(j_k_ff_4_qn), .Q(E), .Qn(j_k_ff_5_qn), .reset(CLR));  // open: preset, en
  J_K_Flip_Flop j_k_ff_6 (.J(E), .clk(CLK_out), .K(j_k_ff_5_qn), .Q(F), .Qn(j_k_ff_6_qn));  // open: preset, en, reset
endmodule
