// Logisim project Exercicio4.circ as structural Verilog: 1 circuit, main circuit main
module main (
  input  in_1,
  input  in_2,
  input  in_3
);

  wire and_1_out, j_k_ff_2_qn, j_k_ff_3_qn, j_k_ff_4_qn, j_k_ff_5_qn, j_k_ff_6_qn, not_1_out, not_2_out;

  J_K_Flip_Flop j_k_ff_1 (.J(in_1), .clk(j_k_ff_2_qn), .K(in_1), .reset(and_1_out));  // open: Q, Qn, preset, en
  J_K_Flip_Flop j_k_ff_2 (
    .J(in_1), .clk(j_k_ff_3_qn), .K(in_1), .Qn(j_k_ff_2_qn), .reset(and_1_out));  // open: Q, preset, en
  and and_1 (and_1_out, not_1_out, j_k_ff_4_qn, not_2_out, j_k_ff_6_qn);
  J_K_Flip_Flop j_k_ff_3 (
    .J(in_1), .clk(j_k_ff_4_qn), .K(in_1), .Qn(j_k_ff_3_qn), .reset(and_1_out));  // open: Q, preset, en
  not not_1 (not_1_out, j_k_ff_3_qn);
  J_K_Flip_Flop j_k_ff_4 (
    .J(in_1), .clk(j_k_ff_5_qn), .K(in_1), .Qn(j_k_ff_4_qn), .reset(and_1_out));  // open: Q, preset, en
  J_K_Flip_Flop j_k_ff_5 (
    .J(in_1), .clk(j_k_ff_6_qn), .K(in_1), .Qn(j_k_ff_5_qn), .reset(and_1_out));  // open: Q, preset, en
  not not_2 (not_2_out, j_k_ff_5_qn);
  J_K_Flip_Flop j_k_ff_6 (.J(in_1), .clk(in_2), .K(in_1), .Qn(j_k_ff_6_qn), .reset(and_1_out));  // open: Q, preset, en
endmodule
