// Logisim project Exemplo0077.circ as structural Verilog: 1 circuit, main circuit main
module main (
  input  \input ,
  input  clear,
  output a,
  output b,
  output c,
  output d,
  output e,
  output f
);

  wire clock_out, j_k_ff_1_qn, j_k_ff_2_qn, j_k_ff_3_qn, j_k_ff_4_qn, j_k_ff_5_qn, j_k_ff_6_qn, not_1_out,
       or_1_out;

  Clock clock (.out(clock_out));
  or or_1 (or_1_out, j_k_ff_6_qn, \input );
  J_K_Flip_Flop j_k_ff_1 (
    .J(or_1_out), .clk(clock_out), .K(not_1_out), .Q(a), .Qn(j_k_ff_1_qn), .reset(clear));  // open: preset, en
  not not_1 (not_1_out, or_1_out);
  J_K_Flip_Flop j_k_ff_2 (
    .J(a), .clk(clock_out), .K(j_k_ff_1_qn), .Q(b), .Qn(j_k_ff_2_qn), .reset(clear));  // open: preset, en
  J_K_Flip_Flop j_k_ff_3 (
    .J(b), .clk(clock_out), .K(j_k_ff_2_qn), .Q(c), .Qn(j_k_ff_3_qn), .reset(clear));  // open: preset, en
  J_K_Flip_Flop j_k_ff_4 (
    .J(c), .clk(clock_out), .K(j_k_ff_3_qn), .Q(d), .Qn(j_k_ff_4_qn), .reset(clear));  // open: preset, en
  J_K_Flip_Flop j_k_ff_5 (
    .J(d), .clk(clock_out), .K(j_k_ff_4_qn), .Q(e), .Qn(j_k_ff_5_qn), .reset(clear));  // open: preset, en
  J_K_Flip_Flop j_k_ff_6 (
    .J(e), .clk(clock_out), .K(j_k_ff_5_qn), .Q(f), .Qn(j_k_ff_6_qn), .reset(clear));  // open: preset, en
endmodule
