// Logisim project circuitos.circ as structural Verilog
module ex01 (
  input  _1,
  input  CLR,
  output a,
  output b,
  output c,
  output d,
  output e
);

  wire CLK_out;

  Clock CLK (.out(CLK_out));
  J_K_Flip_Flop j_k_ff_1 (.J(_1), .clk(b), .K(_1), .Qn(a), .reset(CLR));  // open: Q, preset, en
  J_K_Flip_Flop j_k_ff_2 (.J(_1), .clk(c), .K(_1), .Qn(b), .reset(CLR));  // open: Q, preset, en
  J_K_Flip_Flop j_k_ff_3 (.J(_1), .clk(d), .K(_1), .Qn(c), .reset(CLR));  // open: Q, preset, en
  J_K_Flip_Flop j_k_ff_4 (.J(_1), .clk(e), .K(_1), .Qn(d), .reset(CLR));  // open: Q, preset, en
  J_K_Flip_Flop j_k_ff_5 (.J(_1), .clk(CLK_out), .K(_1), .Qn(e), .reset(CLR));  // open: Q, preset, en
endmodule

module ex02 (
  input  _1,
  input  CLR,
  output a,
  output b,
  output c,
  output d,
  output e
);

  wire CLK_out, j_k_ff_2_q, j_k_ff_3_q, j_k_ff_4_q, j_k_ff_5_q;

  Clock CLK (.out(CLK_out));
  J_K_Flip_Flop j_k_ff_1 (.J(_1), .clk(j_k_ff_2_q), .K(_1), .Qn(a), .reset(CLR));  // open: Q, preset, en
  J_K_Flip_Flop j_k_ff_2 (.J(_1), .clk(j_k_ff_3_q), .K(_1), .Q(j_k_ff_2_q), .Qn(b), .reset(CLR));  // open: preset, en
  J_K_Flip_Flop j_k_ff_3 (.J(_1), .clk(j_k_ff_4_q), .K(_1), .Q(j_k_ff_3_q), .Qn(c), .reset(CLR));  // open: preset, en
  J_K_Flip_Flop j_k_ff_4 (
    .J(CLK_out), .clk(j_k_ff_5_q), .K(CLK_out), .Q(j_k_ff_4_q), .Qn(d), .reset(CLR));  // open: preset, en
  J_K_Flip_Flop j_k_ff_5 (.J(_1), .clk(CLK_out), .K(_1), .Q(j_k_ff_5_q), .Qn(e), .reset(CLR));  // open: preset, en
endmodule

module ex03 (
  input  _1,
  output a,
  output b,
  output c,
  output d,
  output e,
  output f
);

  wire and_1_out, CLK_out, j_k_ff_1_qn, j_k_ff_2_qn, j_k_ff_3_qn, j_k_ff_4_qn, j_k_ff_5_qn, j_k_ff_6_qn,
       not_1_out, not_2_out, not_3_out, not_4_out, not_5_out, or_1_out;

  Clock CLK (.out(CLK_out));
  J_K_Flip_Flop j_k_ff_1 (
    .J(_1), .clk(CLK_out), .K(_1), .Q(f), .Qn(j_k_ff_1_qn), .preset(or_1_out));  // open: en, reset
  not not_1 (not_1_out, _1);
  or or_1 (or_1_out, not_1_out, and_1_out);
  not not_2 (not_2_out, j_k_ff_1_qn);
  and and_1 (and_1_out, not_2_out, j_k_ff_2_qn, j_k_ff_5_qn, not_4_out, not_5_out);
  not not_3 (not_3_out, j_k_ff_3_qn);
  not not_4 (not_4_out, j_k_ff_6_qn);
  not not_5 (not_5_out, j_k_ff_4_qn);
  J_K_Flip_Flop j_k_ff_2 (.J(_1), .clk(f), .K(_1), .Q(e), .Qn(j_k_ff_2_qn), .preset(or_1_out));  // open: en, reset
  J_K_Flip_Flop j_k_ff_3 (.J(_1), .clk(e), .K(_1), .Q(c), .Qn(j_k_ff_3_qn), .preset(or_1_out));  // open: en, reset
  J_K_Flip_Flop j_k_ff_4 (.J(_1), .clk(c), .K(_1), .Q(d), .Qn(j_k_ff_4_qn), .preset(or_1_out));  // open: en, reset
  J_K_Flip_Flop j_k_ff_5 (.J(_1), .clk(d), .K(_1), .Q(b), .Qn(j_k_ff_5_qn), .preset(or_1_out));  // open: en, reset
  J_K_Flip_Flop j_k_ff_6 (.J(_1), .clk(b), .K(_1), .Q(a), .Qn(j_k_ff_6_qn), .preset(or_1_out));  // open: en, reset
endmodule

module ex04 (
  input  _1,
  input  CLR,
  output a,
  output b,
  output c,
  output d,
  output e,
  output f
);

  wire CLK_out, j_k_ff_1_qn, j_k_ff_2_qn, j_k_ff_3_qn, j_k_ff_4_qn, j_k_ff_5_qn, nand_1_out, nand_2_out,
       not_1_out, not_2_out, not_3_out, not_4_out;

  Clock CLK (.out(CLK_out));
  J_K_Flip_Flop j_k_ff_1 (
    .J(_1), .clk(CLK_out), .K(_1), .Q(f), .Qn(j_k_ff_1_qn), .reset(nand_1_out));  // open: preset, en
  nand nand_1 (nand_1_out, CLR, nand_2_out);
  not not_1 (not_1_out, f);
  nand nand_2 (nand_2_out, not_1_out, e, b, not_3_out, not_4_out);
  not not_2 (not_2_out, c);
  not not_3 (not_3_out, a);
  not not_4 (not_4_out, d);
  J_K_Flip_Flop j_k_ff_2 (
    .J(_1), .clk(j_k_ff_1_qn), .K(_1), .Q(e), .Qn(j_k_ff_2_qn), .reset(nand_1_out));  // open: preset, en
  J_K_Flip_Flop j_k_ff_3 (
    .J(_1), .clk(j_k_ff_2_qn), .K(_1), .Q(c), .Qn(j_k_ff_3_qn), .reset(nand_1_out));  // open: preset, en
  J_K_Flip_Flop j_k_ff_4 (
    .J(_1), .clk(j_k_ff_3_qn), .K(_1), .Q(d), .Qn(j_k_ff_4_qn), .reset(nand_1_out));  // open: preset, en
  J_K_Flip_Flop j_k_ff_5 (
    .J(_1), .clk(j_k_ff_4_qn), .K(_1), .Q(b), .Qn(j_k_ff_5_qn), .reset(nand_1_out));  // open: preset, en
  J_K_Flip_Flop j_k_ff_6 (.J(_1), .clk(j_k_ff_5_qn), .K(_1), .Q(a), .reset(nand_1_out));  // open: Qn, preset, en
endmodule

module ex05 (
  input  PULSE,
  input  CLR,
  output a,
  output b,
  output c,
  output d
);

  wire and_1_out, or_1_out, t_ff_2_qn, t_ff_3_qn, t_ff_4_qn;

  or or_1 (or_1_out, CLR, and_1_out);
  and and_1 (and_1_out, a, t_ff_2_qn, t_ff_3_qn, t_ff_4_qn);
  T_Flip_Flop t_ff_1 (.clk(t_ff_2_qn), .T(t_ff_2_qn), .Q(a), .reset(or_1_out));  // open: Qn, preset, en
  T_Flip_Flop t_ff_2 (.clk(t_ff_3_qn), .T(t_ff_3_qn), .Q(b), .Qn(t_ff_2_qn), .reset(or_1_out));  // open: preset, en
  T_Flip_Flop t_ff_3 (.clk(t_ff_4_qn), .T(t_ff_4_qn), .Q(c), .Qn(t_ff_3_qn), .reset(or_1_out));  // open: preset, en
  T_Flip_Flop t_ff_4 (.clk(PULSE), .T(PULSE), .Q(d), .Qn(t_ff_4_qn));  // open: preset, reset, en
endmodule

module ex06 (
  input  INPUT,
  input  CLR,
  output a,
  output b,
  output c,
  output d,
  output e,
  output f
);

  wire CLK_out, j_k_ff_1_qn, j_k_ff_2_qn, j_k_ff_3_qn, j_k_ff_4_qn, j_k_ff_5_qn, not_1_out, or_1_out;

  Clock CLK (.out(CLK_out));
  not not_1 (not_1_out, or_1_out);
  or or_1 (or_1_out, f, INPUT);
  J_K_Flip_Flop j_k_ff_1 (
    .J(or_1_out), .clk(CLK_out), .K(not_1_out), .Q(a), .Qn(j_k_ff_1_qn), .reset(CLR));  // open: preset, en
  J_K_Flip_Flop j_k_ff_2 (
    .J(a), .clk(CLK_out), .K(j_k_ff_1_qn), .Q(b), .Qn(j_k_ff_2_qn), .reset(CLR));  // open: preset, en
  J_K_Flip_Flop j_k_ff_3 (
    .J(b), .clk(CLK_out), .K(j_k_ff_2_qn), .Q(c), .Qn(j_k_ff_3_qn), .reset(CLR));  // open: preset, en
  J_K_Flip_Flop j_k_ff_4 (
    .J(c), .clk(CLK_out), .K(j_k_ff_3_qn), .Q(d), .Qn(j_k_ff_4_qn), .reset(CLR));  // open: preset, en
  J_K_Flip_Flop j_k_ff_5 (
    .J(d), .clk(CLK_out), .K(j_k_ff_4_qn), .Q(e), .Qn(j_k_ff_5_qn), .reset(CLR));  // open: preset, en
  J_K_Flip_Flop j_k_ff_6 (.J(e), .clk(CLK_out), .K(j_k_ff_5_qn), .Q(f), .reset(CLR));  // open: Qn, preset, en
endmodule

module ex07 (
  input  INPUT,
  input  CLR,
  output a,
  output b,
  output c,
  output d,
  output e,
  output f
);

  wire CLK_out, j_k_ff_1_qn, j_k_ff_2_qn, j_k_ff_3_qn, j_k_ff_4_qn, j_k_ff_5_qn, j_k_ff_6_qn, not_1_out,
       or_1_out;

  Clock CLK (.out(CLK_out));
  not not_1 (not_1_out, or_1_out);
  or or_1 (or_1_out, j_k_ff_6_qn, INPUT);
  J_K_Flip_Flop j_k_ff_1 (
    .J(or_1_out), .clk(CLK_out), .K(not_1_out), .Q(a), .Qn(j_k_ff_1_qn), .reset(CLR));  // open: preset, en
  J_K_Flip_Flop j_k_ff_2 (
    .J(a), .clk(CLK_out), .K(j_k_ff_1_qn), .Q(b), .Qn(j_k_ff_2_qn), .reset(CLR));  // open: preset, en
  J_K_Flip_Flop j_k_ff_3 (
    .J(b), .clk(CLK_out), .K(j_k_ff_2_qn), .Q(c), .Qn(j_k_ff_3_qn), .reset(CLR));  // open: preset, en
  J_K_Flip_Flop j_k_ff_4 (
    .J(c), .clk(CLK_out), .K(j_k_ff_3_qn), .Q(d), .Qn(j_k_ff_4_qn), .reset(CLR));  // open: preset, en
  J_K_Flip_Flop j_k_ff_5 (
    .J(d), .clk(CLK_out), .K(j_k_ff_4_qn), .Q(e), .Qn(j_k_ff_5_qn), .reset(CLR));  // open: preset, en
  J_K_Flip_Flop j_k_ff_6 (
    .J(e), .clk(CLK_out), .K(j_k_ff_5_qn), .Q(f), .Qn(j_k_ff_6_qn), .reset(CLR));  // open: preset, en
endmodule
