// Logisim project Exemplo001.circ as structural Verilog: 1 circuit, main circuit main
module main (
  input  Bit,
  input  Clear,
  output out_3,
  output out_4,
  output out_5,
  output out_6,
  output out_7
);

  wire Pulso_out;

  Clock Pulso (.out(Pulso_out));
  J_K_Flip_Flop j_k_ff_1 (.J(Pulso_out), .clk(out_4), .K(Pulso_out), .Qn(out_3), .reset(Clear));  // open: Q, preset, en
  J_K_Flip_Flop j_k_ff_2 (.J(Pulso_out), .clk(out_5), .K(Pulso_out), .Qn(out_4), .reset(Clear));  // open: Q, preset, en
  J_K_Flip_Flop j_k_ff_3 (.J(Pulso_out), .clk(out_6), .K(Pulso_out), .Qn(out_5), .reset(Clear));  // open: Q, preset, en
  J_K_Flip_Flop j_k_ff_4 (.J(Pulso_out), .clk(out_7), .K(Pulso_out), .Qn(out_6), .reset(Clear));  // open: Q, preset, en
  J_K_Flip_Flop j_k_ff_5 (.J(Bit), .clk(Pulso_out), .K(Bit), .Qn(out_7), .reset(Clear));  // open: Q, preset, en
endmodule
