// Logisim project Exemplo002.circ as structural Verilog: 1 circuit, main circuit main
module main (
  input  Entrada,
  input  Clear,
  output Saida_1,
  output Saida_2,
  output Saida_3,
  output Saida_4,
  output Saida_5
);

  wire j_k_ff_2_q, j_k_ff_3_q, j_k_ff_5_q, Pulso_out;

  Clock Pulso (.out(Pulso_out));
  J_K_Flip_Flop j_k_ff_1 (.J(Entrada), .clk(j_k_ff_2_q), .K(Entrada), .Qn(Saida_1));  // open: Q, preset, en, reset
  J_K_Flip_Flop j_k_ff_2 (
    .J(Entrada), .clk(j_k_ff_3_q), .K(Entrada), .Q(j_k_ff_2_q), .Qn(Saida_2));  // open: preset, en, reset
  J_K_Flip_Flop j_k_ff_3 (
    .J(Entrada), .clk(Entrada), .K(Entrada), .Q(j_k_ff_3_q), .Qn(Saida_3));  // open: preset, en, reset
  J_K_Flip_Flop j_k_ff_4 (
    .J(Entrada), .clk(j_k_ff_5_q), .K(Entrada), .Q(Entrada), .Qn(Saida_4));  // open: preset, en, reset
  J_K_Flip_Flop j_k_ff_5 (
    .J(Entrada), .clk(Pulso_out), .K(Entrada), .Q(j_k_ff_5_q), .Qn(Saida_5), .reset(Clear));  // open: preset, en

  // Notes on the sheet:
  //   Contador assincrono crescente de 5 Bits
endmodule
