// Logisim project Exemplo003_Exemplo004.circ as structural Verilog: 1 circuit, main circuit main
module main (
  input  Bit_entrada,
  input  Clear,
  output Saida_1,
  output Saida_2,
  output Saida_3,
  output Saida_4,
  output Saida_5,
  output Saida_6
);

  wire j_k_ff_1_qn, j_k_ff_2_qn, j_k_ff_3_qn, j_k_ff_4_qn, j_k_ff_5_qn, nand_1_out, nand_2_out, not_1_out,
       not_2_out, Pulso_out;

  Clock Pulso (.out(Pulso_out));
  nand nand_1 (nand_1_out, not_1_out, Saida_5, not_2_out, Saida_1, Saida_4);
  J_K_Flip_Flop j_k_ff_1 (
    .J(Bit_entrada), .clk(Pulso_out), .K(Bit_entrada), .Q(Saida_6), .Qn(j_k_ff_1_qn), .reset(nand_2_out));  // open: preset, en
  nand nand_2 (nand_2_out, Clear, nand_1_out);
  not not_1 (not_1_out, Saida_6);
  not not_2 (not_2_out, Saida_2);
  J_K_Flip_Flop j_k_ff_2 (
    .J(Bit_entrada), .clk(j_k_ff_1_qn), .K(Bit_entrada), .Q(Saida_5), .Qn(j_k_ff_2_qn), .reset(nand_2_out));  // open: preset, en
  J_K_Flip_Flop j_k_ff_3 (
    .J(Bit_entrada), .clk(j_k_ff_2_qn), .K(Bit_entrada), .Q(Saida_4), .Qn(j_k_ff_3_qn), .reset(nand_2_out));  // open: preset, en
  J_K_Flip_Flop j_k_ff_4 (
    .J(Bit_entrada), .clk(j_k_ff_3_qn), .K(Bit_entrada), .Q(Saida_3), .Qn(j_k_ff_4_qn), .reset(nand_2_out));  // open: preset, en
  J_K_Flip_Flop j_k_ff_5 (
    .J(Bit_entrada), .clk(j_k_ff_4_qn), .K(Bit_entrada), .Q(Saida_2), .Qn(j_k_ff_5_qn), .reset(nand_2_out));  // open: preset, en
  J_K_Flip_Flop j_k_ff_6 (
    .J(Bit_entrada), .clk(j_k_ff_5_qn), .K(Bit_entrada), .Q(Saida_1), .reset(nand_2_out));  // open: Qn, preset, en

  // Notes on the sheet:
  //   Contador decádico crescente com 6 bits
endmodule
