// Logisim project Exemplo005.circ as structural Verilog: 1 circuit, main circuit main
module main (
  input  Clear,
  output Saida_1,
  output Saida_2,
  output Saida_3,
  output Saida_4
);

  wire and_1_out, not_1_out, not_2_out, or_1_out, Pulso_out, t_ff_2_qn, t_ff_3_qn, t_ff_4_qn;

  Clock Pulso (.out(Pulso_out));
  or or_1 (or_1_out, Clear, and_1_out);
  T_Flip_Flop t_ff_1 (.clk(t_ff_2_qn), .T(t_ff_2_qn), .Q(Saida_1), .reset(or_1_out));  // open: Qn, preset, en
  and and_1 (and_1_out, Saida_1, not_1_out, not_2_out, Saida_4);
  T_Flip_Flop t_ff_2 (
    .clk(t_ff_3_qn), .T(t_ff_3_qn), .Q(Saida_2), .Qn(t_ff_2_qn), .reset(or_1_out));  // open: preset, en
  not not_1 (not_1_out, Saida_2);
  not not_2 (not_2_out, Saida_3);
  T_Flip_Flop t_ff_3 (
    .clk(t_ff_4_qn), .T(t_ff_4_qn), .Q(Saida_3), .Qn(t_ff_3_qn), .reset(or_1_out));  // open: preset, en
  T_Flip_Flop t_ff_4 (
    .clk(Pulso_out), .T(Pulso_out), .Q(Saida_4), .Qn(t_ff_4_qn), .reset(or_1_out));  // open: preset, en

  // Notes on the sheet:
  //   Contador módulo 10b assincrono com FLIP FLOP tipo T
endmodule
