// Logisim project Exercicio01.circ as structural Verilog: 1 circuit, main circuit main
module main (
  input  Pulse,
  input  _1,
  input  Clk,
  output A,
  output B,
  output C,
  output D,
  output E
);

  J_K_Flip_Flop j_k_ff_1 (.J(_1), .clk(B), .K(_1), .Qn(A), .reset(Clk));  // open: Q, preset, en
  J_K_Flip_Flop j_k_ff_2 (.J(_1), .clk(C), .K(_1), .Qn(B), .reset(Clk));  // open: Q, preset, en
  J_K_Flip_Flop j_k_ff_3 (.J(_1), .clk(D), .K(_1), .Qn(C), .reset(Clk));  // open: Q, preset, en
  J_K_Flip_Flop j_k_ff_4 (.J(_1), .clk(E), .K(_1), .Qn(D), .reset(Clk));  // open: Q, preset, en
  J_K_Flip_Flop j_k_ff_5 (.J(_1), .clk(Pulse), .K(_1), .Qn(E), .reset(Clk));  // open: Q, preset, en
endmodule
