// Logisim project Exercicio02.circ as structural Verilog: 1 circuit, main circuit main
module main (
  input  Pulse,
  input  _1,
  input  Clk,
  output A,
  output B,
  output C,
  output D,
  output E
);

  wire j_k_ff_2_q, j_k_ff_3_q, j_k_ff_4_q, j_k_ff_5_q;

  J_K_Flip_Flop j_k_ff_1 (.J(_1), .clk(j_k_ff_2_q), .K(_1), .Qn(A), .reset(Clk));  // open: Q, preset, en
  J_K_Flip_Flop j_k_ff_2 (.J(_1), .clk(j_k_ff_3_q), .K(_1), .Q(j_k_ff_2_q), .Qn(B), .reset(Clk));  // open: preset, en
  J_K_Flip_Flop j_k_ff_3 (.J(_1), .clk(j_k_ff_4_q), .K(_1), .Q(j_k_ff_3_q), .Qn(C), .reset(Clk));  // open: preset, en
  J_K_Flip_Flop j_k_ff_4 (.J(_1), .clk(j_k_ff_5_q), .K(_1), .Q(j_k_ff_4_q), .Qn(D), .reset(Clk));  // open: preset, en
  J_K_Flip_Flop j_k_ff_5 (.J(_1), .clk(Pulse), .K(_1), .Q(j_k_ff_5_q), .Qn(E), .reset(Clk));  // open: preset, en
endmodule
