// Logisim project circuito01.circ as structural Verilog: 1 circuit, main circuit main
module main (
  input  data,
  input  clr,
  output s4,
  output s3,
  output s2,
  output s1,
  output s0
);

  wire clk_out;

  Clock clk (.out(clk_out));
  J_K_Flip_Flop j_k_ff_1 (.J(data), .clk(s3), .K(data), .Qn(s4), .reset(clr));  // open: Q, preset, en
  J_K_Flip_Flop j_k_ff_2 (.J(data), .clk(s2), .K(data), .Qn(s3), .reset(clr));  // open: Q, preset, en
  J_K_Flip_Flop j_k_ff_3 (.J(data), .clk(s1), .K(data), .Qn(s2), .reset(clr));  // open: Q, preset, en
  J_K_Flip_Flop j_k_ff_4 (.J(data), .clk(s0), .K(data), .Qn(s1), .reset(clr));  // open: Q, preset, en
  J_K_Flip_Flop j_k_ff_5 (.J(data), .clk(clk_out), .K(data), .Qn(s0), .reset(clr));  // open: Q, preset, en
endmodule
