// Logisim project circuito02.circ as structural Verilog: 1 circuit, main circuit main
module main (
  input  data,
  input  clr,
  output s4,
  output s3,
  output s2,
  output s1,
  output s0
);

  wire clk_out, j_k_ff_2_q, j_k_ff_3_q, j_k_ff_4_q, j_k_ff_5_q;

  Clock clk (.out(clk_out));
  J_K_Flip_Flop j_k_ff_1 (.J(data), .clk(j_k_ff_2_q), .K(data), .Qn(s4), .reset(clr));  // open: Q, preset, en
  J_K_Flip_Flop j_k_ff_2 (
    .J(data), .clk(j_k_ff_3_q), .K(data), .Q(j_k_ff_2_q), .Qn(s3), .reset(clr));  // open: preset, en
  J_K_Flip_Flop j_k_ff_3 (
    .J(data), .clk(j_k_ff_4_q), .K(data), .Q(j_k_ff_3_q), .Qn(s2), .reset(clr));  // open: preset, en
  J_K_Flip_Flop j_k_ff_4 (
    .J(data), .clk(j_k_ff_5_q), .K(data), .Q(j_k_ff_4_q), .Qn(s1), .reset(clr));  // open: preset, en
  J_K_Flip_Flop j_k_ff_5 (.J(data), .clk(clk_out), .K(data), .Q(j_k_ff_5_q), .Qn(s0), .reset(clr));  // open: preset, en
endmodule
