// Logisim project circuito03.circ as structural Verilog: 1 circuit, main circuit main
module main (
  input  data,
  output s5,
  output s4,
  output s3,
  output s2,
  output s1,
  output s0
);

  wire and_1_out, clk_out, j_k_ff_1_qn, j_k_ff_2_qn, j_k_ff_3_qn, j_k_ff_4_qn, j_k_ff_5_qn, j_k_ff_6_qn,
       not_1_out, or_1_out;

  Clock clk (.out(clk_out));
  not not_1 (not_1_out, data);
  and and_1 (and_1_out, ~j_k_ff_1_qn, j_k_ff_2_qn, ~j_k_ff_3_qn, j_k_ff_4_qn, ~j_k_ff_5_qn, ~j_k_ff_6_qn);  // AND_Gate
  J_K_Flip_Flop j_k_ff_1 (
    .J(data), .clk(clk_out), .K(data), .Q(s0), .Qn(j_k_ff_1_qn), .preset(or_1_out));  // open: en, reset
  or or_1 (or_1_out, not_1_out, and_1_out);
  J_K_Flip_Flop j_k_ff_2 (
    .J(data), .clk(s0), .K(data), .Q(s1), .Qn(j_k_ff_2_qn), .preset(or_1_out));  // open: en, reset
  J_K_Flip_Flop j_k_ff_3 (
    .J(data), .clk(s1), .K(data), .Q(s2), .Qn(j_k_ff_3_qn), .preset(or_1_out));  // open: en, reset
  J_K_Flip_Flop j_k_ff_4 (
    .J(data), .clk(s2), .K(data), .Q(s3), .Qn(j_k_ff_4_qn), .preset(or_1_out));  // open: en, reset
  J_K_Flip_Flop j_k_ff_5 (
    .J(data), .clk(s3), .K(data), .Q(s4), .Qn(j_k_ff_5_qn), .preset(or_1_out));  // open: en, reset
  J_K_Flip_Flop j_k_ff_6 (
    .J(data), .clk(s4), .K(data), .Q(s5), .Qn(j_k_ff_6_qn), .preset(or_1_out));  // open: en, reset
endmodule
