// Logisim project circuito04.circ as structural Verilog: 1 circuit, main circuit main
module main (
  input  data,
  input  clr,
  output s5,
  output s4,
  output s3,
  output s2,
  output s1,
  output s0
);

  wire clk_out, j_k_ff_1_qn, j_k_ff_2_qn, j_k_ff_3_qn, j_k_ff_4_qn, j_k_ff_5_qn, nand_1_out, nand_2_out;

  Clock clk (.out(clk_out));
  nand nand_1 (nand_1_out, ~s0, s1, ~s2, s3, ~s4, ~s5);  // NAND_Gate
  J_K_Flip_Flop j_k_ff_1 (
    .J(data), .clk(clk_out), .K(data), .Q(s0), .Qn(j_k_ff_1_qn), .reset(nand_2_out));  // open: preset, en
  nand nand_2 (nand_2_out, clr, nand_1_out);
  J_K_Flip_Flop j_k_ff_2 (
    .J(data), .clk(j_k_ff_1_qn), .K(data), .Q(s1), .Qn(j_k_ff_2_qn), .reset(nand_2_out));  // open: preset, en
  J_K_Flip_Flop j_k_ff_3 (
    .J(data), .clk(j_k_ff_2_qn), .K(data), .Q(s2), .Qn(j_k_ff_3_qn), .reset(nand_2_out));  // open: preset, en
  J_K_Flip_Flop j_k_ff_4 (
    .J(data), .clk(j_k_ff_3_qn), .K(data), .Q(s3), .Qn(j_k_ff_4_qn), .reset(nand_2_out));  // open: preset, en
  J_K_Flip_Flop j_k_ff_5 (
    .J(data), .clk(j_k_ff_4_qn), .K(data), .Q(s4), .Qn(j_k_ff_5_qn), .reset(nand_2_out));  // open: preset, en
  J_K_Flip_Flop j_k_ff_6 (.J(data), .clk(j_k_ff_5_qn), .K(data), .Q(s5), .reset(nand_2_out));  // open: Qn, preset, en
endmodule
