// Logisim project circuito05.circ as structural Verilog: 1 circuit, main circuit main
module main (
  input  data,
  input  clr,
  output s3,
  output s2,
  output s1,
  output s0
);

  wire and_1_out, or_1_out, t_ff_2_qn, t_ff_3_qn, t_ff_4_qn;

  or or_1 (or_1_out, clr, and_1_out);
  and and_1 (and_1_out, s3, ~s2, s1, ~s0);  // AND_Gate
  T_Flip_Flop t_ff_1 (.clk(t_ff_2_qn), .T(t_ff_2_qn), .Q(s3), .reset(or_1_out));  // open: Qn, preset, en
  T_Flip_Flop t_ff_2 (.clk(t_ff_3_qn), .T(t_ff_3_qn), .Q(s2), .Qn(t_ff_2_qn), .reset(or_1_out));  // open: preset, en
  T_Flip_Flop t_ff_3 (.clk(t_ff_4_qn), .T(t_ff_4_qn), .Q(s1), .Qn(t_ff_3_qn), .reset(or_1_out));  // open: preset, en
  T_Flip_Flop t_ff_4 (.clk(data), .T(data), .Q(s0), .Qn(t_ff_4_qn), .reset(or_1_out));  // open: preset, en
endmodule
