// Logisim project circuito07.circ as structural Verilog: 1 circuit, main circuit main
module main (
  input  data,
  input  clr,
  output s5,
  output s4,
  output s3,
  output s2,
  output s1,
  output s0
);

  wire clk_out, j_k_ff_6_qn, not_1_out, not_2_out, not_3_out, not_4_out, not_5_out, not_6_out, or_1_out;

  Clock clk (.out(clk_out));
  or or_1 (or_1_out, data, j_k_ff_6_qn);
  J_K_Flip_Flop j_k_ff_1 (.J(or_1_out), .clk(clk_out), .K(not_1_out), .Q(s5), .reset(clr));  // open: Qn, preset, en
  not not_1 (not_1_out, or_1_out);
  J_K_Flip_Flop j_k_ff_2 (.J(s5), .clk(clk_out), .K(not_2_out), .Q(s4), .reset(clr));  // open: Qn, preset, en
  not not_2 (not_2_out, s5);
  J_K_Flip_Flop j_k_ff_3 (.J(s4), .clk(clk_out), .K(not_3_out), .Q(s3), .reset(clr));  // open: Qn, preset, en
  not not_3 (not_3_out, s4);
  not not_4 (not_4_out, s3);
  J_K_Flip_Flop j_k_ff_4 (.J(s3), .clk(clk_out), .K(not_4_out), .Q(s2), .reset(clr));  // open: Qn, preset, en
  not not_5 (not_5_out, s2);
  J_K_Flip_Flop j_k_ff_5 (.J(s2), .clk(clk_out), .K(not_5_out), .Q(s1), .reset(clr));  // open: Qn, preset, en
  not not_6 (not_6_out, s1);
  J_K_Flip_Flop j_k_ff_6 (.J(s1), .clk(clk_out), .K(not_6_out), .Q(s0), .Qn(j_k_ff_6_qn));  // open: preset, en, reset
endmodule
