// Logisim project Exercicio004.circ as structural Verilog: 1 circuit, main circuit main
module main (
  input  pulse,
  input  CLR,
  output a,
  output b,
  output c,
  output d,
  output e
);

  wire j_k_ff_1_qn, j_k_ff_2_qn, j_k_ff_3_qn, j_k_ff_4_qn, nand_1_out, nand_2_out, not_1_out, not_2_out;

  J_K_Flip_Flop j_k_ff_1 (
    .J(1'b1), .clk(pulse), .K(1'b1), .Q(e), .Qn(j_k_ff_1_qn), .reset(nand_1_out));  // open: preset, en
  nand nand_1 (nand_1_out, CLR, nand_2_out);
  not not_1 (not_1_out, e);
  nand nand_2 (nand_2_out, not_1_out, d, not_2_out, b, a);
  not not_2 (not_2_out, c);
  J_K_Flip_Flop j_k_ff_2 (
    .J(1'b1), .clk(j_k_ff_1_qn), .K(1'b1), .Q(d), .Qn(j_k_ff_2_qn), .reset(nand_1_out));  // open: preset, en
  J_K_Flip_Flop j_k_ff_3 (
    .J(1'b1), .clk(j_k_ff_2_qn), .K(1'b1), .Q(c), .Qn(j_k_ff_3_qn), .reset(nand_1_out));  // open: preset, en
  J_K_Flip_Flop j_k_ff_4 (
    .J(1'b1), .clk(j_k_ff_3_qn), .K(1'b1), .Q(b), .Qn(j_k_ff_4_qn), .reset(nand_1_out));  // open: preset, en
  J_K_Flip_Flop j_k_ff_5 (.J(1'b1), .clk(j_k_ff_4_qn), .K(1'b1), .Q(a), .reset(nand_1_out));  // open: Qn, preset, en

  // Notes on the sheet:
  //   Fernando Silva
endmodule
