// Logisim project Circuitos.circ as structural Verilog
module Exercicio01 (
  input  data,
  input  clr,
  output s4,
  output s3,
  output s2,
  output s1,
  output s0
);

  wire clk_out;

  Clock clk (.out(clk_out));
  J_K_Flip_Flop j_k_ff_1 (.J(data), .clk(s3), .K(data), .Qn(s4), .reset(clr));  // open: Q, preset, en
  J_K_Flip_Flop j_k_ff_2 (.J(data), .clk(s2), .K(data), .Qn(s3), .reset(clr));  // open: Q, preset, en
  J_K_Flip_Flop j_k_ff_3 (.J(data), .clk(s1), .K(data), .Qn(s2), .reset(clr));  // open: Q, preset, en
  J_K_Flip_Flop j_k_ff_4 (.J(data), .clk(s0), .K(data), .Qn(s1), .reset(clr));  // open: Q, preset, en
  J_K_Flip_Flop j_k_ff_5 (.J(data), .clk(clk_out), .K(data), .Qn(s0), .reset(clr));  // open: Q, preset, en
endmodule

module Exercicio02 (
  input  data,
  input  clr,
  output s4,
  output s3,
  output s2,
  output s1,
  output s0
);

  wire clk_out, j_k_ff_2_q, j_k_ff_3_q, j_k_ff_4_q, j_k_ff_5_q;

  Clock clk (.out(clk_out));
  J_K_Flip_Flop j_k_ff_1 (.J(data), .clk(j_k_ff_2_q), .K(data), .Qn(s4), .reset(clr));  // open: Q, preset, en
  J_K_Flip_Flop j_k_ff_2 (
    .J(data), .clk(j_k_ff_3_q), .K(data), .Q(j_k_ff_2_q), .Qn(s3), .reset(clr));  // open: preset, en
  J_K_Flip_Flop j_k_ff_3 (
    .J(data), .clk(j_k_ff_4_q), .K(data), .Q(j_k_ff_3_q), .Qn(s2), .reset(clr));  // open: preset, en
  J_K_Flip_Flop j_k_ff_4 (
    .J(data), .clk(j_k_ff_5_q), .K(data), .Q(j_k_ff_4_q), .Qn(s1), .reset(clr));  // open: preset, en
  J_K_Flip_Flop j_k_ff_5 (.J(data), .clk(clk_out), .K(data), .Q(j_k_ff_5_q), .Qn(s0), .reset(clr));  // open: preset, en
endmodule

module Exercicio03 (
  input  data,
  output s5,
  output s4,
  output s3,
  output s2,
  output s1,
  output s0
);

  wire and_1_out, clk_out, j_k_ff_1_qn, j_k_ff_2_qn, j_k_ff_3_qn, j_k_ff_4_qn, j_k_ff_5_qn, j_k_ff_6_qn,
       not_1_out, or_1_out;

  Clock clk (.out(clk_out));
  not not_1 (not_1_out, data);
  and and_1 (and_1_out, ~j_k_ff_1_qn, j_k_ff_2_qn, ~j_k_ff_3_qn, j_k_ff_4_qn, ~j_k_ff_5_qn, ~j_k_ff_6_qn);  // AND_Gate
  J_K_Flip_Flop j_k_ff_1 (
    .J(data), .clk(clk_out), .K(data), .Q(s0), .Qn(j_k_ff_1_qn), .preset(or_1_out));  // open: en, reset
  or or_1 (or_1_out, not_1_out, and_1_out);
  J_K_Flip_Flop j_k_ff_2 (
    .J(data), .clk(s0), .K(data), .Q(s1), .Qn(j_k_ff_2_qn), .preset(or_1_out));  // open: en, reset
  J_K_Flip_Flop j_k_ff_3 (
    .J(data), .clk(s1), .K(data), .Q(s2), .Qn(j_k_ff_3_qn), .preset(or_1_out));  // open: en, reset
  J_K_Flip_Flop j_k_ff_4 (
    .J(data), .clk(s2), .K(data), .Q(s3), .Qn(j_k_ff_4_qn), .preset(or_1_out));  // open: en, reset
  J_K_Flip_Flop j_k_ff_5 (
    .J(data), .clk(s3), .K(data), .Q(s4), .Qn(j_k_ff_5_qn), .preset(or_1_out));  // open: en, reset
  J_K_Flip_Flop j_k_ff_6 (
    .J(data), .clk(s4), .K(data), .Q(s5), .Qn(j_k_ff_6_qn), .preset(or_1_out));  // open: en, reset
endmodule

module Exercicio04 (
  input  data,
  input  clr,
  output s5,
  output s4,
  output s3,
  output s2,
  output s1,
  output s0
);

  wire clk_out, j_k_ff_1_qn, j_k_ff_2_qn, j_k_ff_3_qn, j_k_ff_4_qn, j_k_ff_5_qn, nand_1_out, nand_2_out;

  Clock clk (.out(clk_out));
  nand nand_1 (nand_1_out, ~s0, s1, ~s2, s3, ~s4, ~s5);  // NAND_Gate
  J_K_Flip_Flop j_k_ff_1 (
    .J(data), .clk(clk_out), .K(data), .Q(s0), .Qn(j_k_ff_1_qn), .reset(nand_2_out));  // open: preset, en
  nand nand_2 (nand_2_out, clr, nand_1_out);
  J_K_Flip_Flop j_k_ff_2 (
    .J(data), .clk(j_k_ff_1_qn), .K(data), .Q(s1), .Qn(j_k_ff_2_qn), .reset(nand_2_out));  // open: preset, en
  J_K_Flip_Flop j_k_ff_3 (
    .J(data), .clk(j_k_ff_2_qn), .K(data), .Q(s2), .Qn(j_k_ff_3_qn), .reset(nand_2_out));  // open: preset, en
  J_K_Flip_Flop j_k_ff_4 (
    .J(data), .clk(j_k_ff_3_qn), .K(data), .Q(s3), .Qn(j_k_ff_4_qn), .reset(nand_2_out));  // open: preset, en
  J_K_Flip_Flop j_k_ff_5 (
    .J(data), .clk(j_k_ff_4_qn), .K(data), .Q(s4), .Qn(j_k_ff_5_qn), .reset(nand_2_out));  // open: preset, en
  J_K_Flip_Flop j_k_ff_6 (.J(data), .clk(j_k_ff_5_qn), .K(data), .Q(s5), .reset(nand_2_out));  // open: Qn, preset, en
endmodule

module Exercicio05 (
  input  data,
  input  clr,
  output s3,
  output s2,
  output s1,
  output s0
);

  wire and_1_out, or_1_out, t_ff_2_qn, t_ff_3_qn, t_ff_4_qn;

  or or_1 (or_1_out, clr, and_1_out);
  and and_1 (and_1_out, s3, ~s2, s1, ~s0);  // AND_Gate
  T_Flip_Flop t_ff_1 (.clk(t_ff_2_qn), .T(t_ff_2_qn), .Q(s3), .reset(or_1_out));  // open: Qn, preset, en
  T_Flip_Flop t_ff_2 (.clk(t_ff_3_qn), .T(t_ff_3_qn), .Q(s2), .Qn(t_ff_2_qn), .reset(or_1_out));  // open: preset, en
  T_Flip_Flop t_ff_3 (.clk(t_ff_4_qn), .T(t_ff_4_qn), .Q(s1), .Qn(t_ff_3_qn), .reset(or_1_out));  // open: preset, en
  T_Flip_Flop t_ff_4 (.clk(data), .T(data), .Q(s0), .Qn(t_ff_4_qn), .reset(or_1_out));  // open: preset, en
endmodule

module Exercicio06 (
  input  data,
  input  clr,
  output s5,
  output s4,
  output s3,
  output s2,
  output s1,
  output s0
);

  wire clk_out, not_1_out, not_2_out, not_3_out, not_4_out, not_5_out, not_6_out, or_1_out;

  Clock clk (.out(clk_out));
  not not_1 (not_1_out, or_1_out);
  or or_1 (or_1_out, s0, data);
  J_K_Flip_Flop j_k_ff_1 (.J(or_1_out), .clk(clk_out), .K(not_1_out), .Q(s5), .reset(clr));  // open: Qn, preset, en
  J_K_Flip_Flop j_k_ff_2 (.J(s5), .clk(clk_out), .K(not_2_out), .Q(s4), .reset(clr));  // open: Qn, preset, en
  not not_2 (not_2_out, s5);
  not not_3 (not_3_out, s4);
  J_K_Flip_Flop j_k_ff_3 (.J(s4), .clk(clk_out), .K(not_3_out), .Q(s3), .reset(clr));  // open: Qn, preset, en
  not not_4 (not_4_out, s3);
  J_K_Flip_Flop j_k_ff_4 (.J(s3), .clk(clk_out), .K(not_4_out), .Q(s2), .reset(clr));  // open: Qn, preset, en
  not not_5 (not_5_out, s2);
  J_K_Flip_Flop j_k_ff_5 (.J(s2), .clk(clk_out), .K(not_5_out), .Q(s1), .reset(clr));  // open: Qn, preset, en
  J_K_Flip_Flop j_k_ff_6 (.J(s1), .clk(clk_out), .K(not_6_out), .Q(s0), .reset(clr));  // open: Qn, preset, en
  not not_6 (not_6_out, s1);
endmodule

module Exercicio07 (
  input  data,
  input  clr,
  output s5,
  output s4,
  output s3,
  output s2,
  output s1,
  output s0
);

  wire clk_out, j_k_ff_6_qn, not_1_out, not_2_out, not_3_out, not_4_out, not_5_out, not_6_out, or_1_out;

  Clock clk (.out(clk_out));
  or or_1 (or_1_out, data, j_k_ff_6_qn);
  J_K_Flip_Flop j_k_ff_1 (.J(or_1_out), .clk(clk_out), .K(not_1_out), .Q(s5), .reset(clr));  // open: Qn, preset, en
  not not_1 (not_1_out, or_1_out);
  J_K_Flip_Flop j_k_ff_2 (.J(s5), .clk(clk_out), .K(not_2_out), .Q(s4), .reset(clr));  // open: Qn, preset, en
  not not_2 (not_2_out, s5);
  J_K_Flip_Flop j_k_ff_3 (.J(s4), .clk(clk_out), .K(not_3_out), .Q(s3), .reset(clr));  // open: Qn, preset, en
  not not_3 (not_3_out, s4);
  not not_4 (not_4_out, s3);
  J_K_Flip_Flop j_k_ff_4 (.J(s3), .clk(clk_out), .K(not_4_out), .Q(s2), .reset(clr));  // open: Qn, preset, en
  not not_5 (not_5_out, s2);
  J_K_Flip_Flop j_k_ff_5 (.J(s2), .clk(clk_out), .K(not_5_out), .Q(s1), .reset(clr));  // open: Qn, preset, en
  not not_6 (not_6_out, s1);
  J_K_Flip_Flop j_k_ff_6 (.J(s1), .clk(clk_out), .K(not_6_out), .Q(s0), .Qn(j_k_ff_6_qn));  // open: preset, en, reset
endmodule
