// Logisim project Circuitos.circ as structural Verilog
module Exercicio01 (
  input  Pulse,
  input  _1,
  input  Clear,
  output a,
  output b,
  output c,
  output d,
  output e
);

  J_K_Flip_Flop j_k_ff_1 (.J(_1), .clk(b), .K(_1), .Qn(a), .reset(Clear));  // open: Q, preset, en
  J_K_Flip_Flop j_k_ff_2 (.J(_1), .clk(c), .K(_1), .Qn(b), .reset(Clear));  // open: Q, preset, en
  J_K_Flip_Flop j_k_ff_3 (.J(_1), .clk(d), .K(_1), .Qn(c), .reset(Clear));  // open: Q, preset, en
  J_K_Flip_Flop j_k_ff_4 (.J(_1), .clk(e), .K(_1), .Qn(d), .reset(Clear));  // open: Q, preset, en
  J_K_Flip_Flop j_k_ff_5 (.J(_1), .clk(Pulse), .K(_1), .Qn(e), .reset(Clear));  // open: Q, preset, en

  // Notes on the sheet:
  //   Exercicio01 - Djonatas Tulio Rodrigues Costa - 440954
endmodule

module Exercicio02 (
  input  Pulse,
  input  _1,
  input  Clear,
  output a,
  output b,
  output c,
  output d,
  output e
);

  wire j_k_ff_2_q, j_k_ff_3_q, j_k_ff_4_q, j_k_ff_5_q;

  J_K_Flip_Flop j_k_ff_1 (.J(_1), .clk(j_k_ff_2_q), .K(_1), .Qn(a), .reset(Clear));  // open: Q, preset, en
  J_K_Flip_Flop j_k_ff_2 (.J(_1), .clk(j_k_ff_3_q), .K(_1), .Q(j_k_ff_2_q), .Qn(b), .reset(Clear));  // open: preset, en
  J_K_Flip_Flop j_k_ff_3 (.J(_1), .clk(j_k_ff_4_q), .K(_1), .Q(j_k_ff_3_q), .Qn(c), .reset(Clear));  // open: preset, en
  J_K_Flip_Flop j_k_ff_4 (.J(_1), .clk(j_k_ff_5_q), .K(_1), .Q(j_k_ff_4_q), .Qn(d), .reset(Clear));  // open: preset, en
  J_K_Flip_Flop j_k_ff_5 (.J(_1), .clk(Pulse), .K(_1), .Q(j_k_ff_5_q), .Qn(e), .reset(Clear));  // open: preset, en

  // Notes on the sheet:
  //   Exercicio02 - Djonatas Tulio Rodrigues Costa - 440954
endmodule

module Exercicio03 (
  input  _1,
  input  Pulse,
  input  Clear,
  output a,
  output b,
  output c,
  output d,
  output e,
  output f
);

  wire j_k_ff_1_qn, j_k_ff_2_qn, j_k_ff_3_qn, j_k_ff_4_qn, j_k_ff_5_qn, nand_1_out, nand_2_out;

  nand nand_1 (nand_1_out, ~f, e, ~d, c, ~b, ~a);  // NAND_Gate
  nand nand_2 (nand_2_out, Clear, nand_1_out);
  J_K_Flip_Flop j_k_ff_1 (
    .J(_1), .clk(Pulse), .K(_1), .Q(f), .Qn(j_k_ff_1_qn), .reset(nand_2_out));  // open: preset, en
  J_K_Flip_Flop j_k_ff_2 (
    .J(_1), .clk(j_k_ff_1_qn), .K(_1), .Q(e), .Qn(j_k_ff_2_qn), .reset(nand_2_out));  // open: preset, en
  J_K_Flip_Flop j_k_ff_3 (
    .J(_1), .clk(j_k_ff_2_qn), .K(_1), .Q(d), .Qn(j_k_ff_3_qn), .reset(nand_2_out));  // open: preset, en
  J_K_Flip_Flop j_k_ff_4 (
    .J(_1), .clk(j_k_ff_3_qn), .K(_1), .Q(c), .Qn(j_k_ff_4_qn), .reset(nand_2_out));  // open: preset, en
  J_K_Flip_Flop j_k_ff_5 (
    .J(_1), .clk(j_k_ff_4_qn), .K(_1), .Q(b), .Qn(j_k_ff_5_qn), .reset(nand_2_out));  // open: preset, en
  J_K_Flip_Flop j_k_ff_6 (.J(_1), .clk(j_k_ff_5_qn), .K(_1), .Q(a), .reset(nand_2_out));  // open: Qn, preset, en

  // Notes on the sheet:
  //   Exercicio03 - Djonatas Tulio Rodrigues Costa - 440954
endmodule

module Exercicio04 (
  input  _1,
  input  Pulse,
  input  Clear,
  output a,
  output b,
  output c,
  output d,
  output e,
  output f
);

  wire and_1_out, j_k_ff_1_qn, j_k_ff_2_qn, j_k_ff_3_qn, j_k_ff_4_qn, j_k_ff_5_qn, j_k_ff_6_qn, or_1_out;

  or or_1 (or_1_out, ~_1, and_1_out);  // OR_Gate
  and and_1 (and_1_out, ~j_k_ff_1_qn, j_k_ff_2_qn, ~j_k_ff_3_qn, j_k_ff_4_qn, ~j_k_ff_5_qn, ~j_k_ff_6_qn);  // AND_Gate
  J_K_Flip_Flop j_k_ff_1 (
    .J(_1), .clk(Pulse), .K(_1), .Q(f), .Qn(j_k_ff_1_qn), .preset(or_1_out), .reset(Clear));  // open: en
  J_K_Flip_Flop j_k_ff_2 (
    .J(_1), .clk(f), .K(_1), .Q(e), .Qn(j_k_ff_2_qn), .preset(or_1_out), .reset(Clear));  // open: en
  J_K_Flip_Flop j_k_ff_3 (
    .J(_1), .clk(e), .K(_1), .Q(d), .Qn(j_k_ff_3_qn), .preset(or_1_out), .reset(Clear));  // open: en
  J_K_Flip_Flop j_k_ff_4 (
    .J(_1), .clk(d), .K(_1), .Q(c), .Qn(j_k_ff_4_qn), .preset(or_1_out), .reset(Clear));  // open: en
  J_K_Flip_Flop j_k_ff_5 (
    .J(_1), .clk(c), .K(_1), .Q(b), .Qn(j_k_ff_5_qn), .preset(or_1_out), .reset(Clear));  // open: en
  J_K_Flip_Flop j_k_ff_6 (
    .J(_1), .clk(b), .K(_1), .Q(a), .Qn(j_k_ff_6_qn), .preset(or_1_out), .reset(Clear));  // open: en

  // Notes on the sheet:
  //   Exercicio04 - Djonatas Tulio Rodrigues Costa - 440954
endmodule

module Exercicio05 (
  input  Pulse,
  input  Clear,
  output a,
  output b,
  output c,
  output d
);

  wire and_1_out, or_1_out, t_ff_2_qn, t_ff_3_qn, t_ff_4_qn;

  or or_1 (or_1_out, Clear, and_1_out);
  and and_1 (and_1_out, a, ~b, c, ~d);  // AND_Gate
  T_Flip_Flop t_ff_1 (.clk(t_ff_2_qn), .T(t_ff_2_qn), .Q(a), .reset(or_1_out));  // open: Qn, preset, en
  T_Flip_Flop t_ff_2 (.clk(t_ff_3_qn), .T(t_ff_3_qn), .Q(b), .Qn(t_ff_2_qn), .reset(or_1_out));  // open: preset, en
  T_Flip_Flop t_ff_3 (.clk(t_ff_4_qn), .T(t_ff_4_qn), .Q(c), .Qn(t_ff_3_qn), .reset(or_1_out));  // open: preset, en
  T_Flip_Flop t_ff_4 (.clk(Pulse), .T(Pulse), .Q(d), .Qn(t_ff_4_qn), .reset(or_1_out));  // open: preset, en

  // Notes on the sheet:
  //   Exercicio05 - Djonatas Tulio Rodrigues Costa - 440954
endmodule
