// Logisim project guai09.circ as structural Verilog
module _091 (
  input  in_1,
  input  in_2,
  output out_3,
  output out_4,
  output out_5,
  output out_6,
  output out_7
);

  wire clock_1_out;

  Clock clock_1 (.out(clock_1_out));
  J_K_Flip_Flop j_k_ff_1 (.J(in_1), .clk(clock_1_out), .K(in_1), .Qn(out_7), .reset(in_2));  // open: Q, preset, en
  J_K_Flip_Flop j_k_ff_2 (.J(in_1), .clk(out_7), .K(in_1), .Qn(out_6), .reset(in_2));  // open: Q, preset, en
  J_K_Flip_Flop j_k_ff_3 (.J(in_1), .clk(out_6), .K(in_1), .Qn(out_5), .reset(in_2));  // open: Q, preset, en
  J_K_Flip_Flop j_k_ff_4 (.J(in_1), .clk(out_5), .K(in_1), .Qn(out_4), .reset(in_2));  // open: Q, preset, en
  J_K_Flip_Flop j_k_ff_5 (.J(in_1), .clk(out_4), .K(in_1), .Qn(out_3), .reset(in_2));  // open: Q, preset, en

  // Notes on the sheet:
  //   A
  //   B
  //   C
  //   D
  //   E
endmodule

module _092 (
  input  in_1,
  input  in_2,
  output out_3,
  output out_4,
  output out_5,
  output out_6,
  output out_7
);

  wire clock_1_out, j_k_ff_1_q, j_k_ff_2_q, j_k_ff_3_q, j_k_ff_4_q;

  Clock clock_1 (.out(clock_1_out));
  J_K_Flip_Flop j_k_ff_1 (
    .J(in_1), .clk(clock_1_out), .K(in_1), .Q(j_k_ff_1_q), .Qn(out_7), .reset(in_2));  // open: preset, en
  J_K_Flip_Flop j_k_ff_2 (
    .J(in_1), .clk(j_k_ff_1_q), .K(in_1), .Q(j_k_ff_2_q), .Qn(out_6), .reset(in_2));  // open: preset, en
  J_K_Flip_Flop j_k_ff_3 (
    .J(in_1), .clk(j_k_ff_2_q), .K(in_1), .Q(j_k_ff_3_q), .Qn(out_5), .reset(in_2));  // open: preset, en
  J_K_Flip_Flop j_k_ff_4 (
    .J(in_1), .clk(j_k_ff_3_q), .K(in_1), .Q(j_k_ff_4_q), .Qn(out_4), .reset(in_2));  // open: preset, en
  J_K_Flip_Flop j_k_ff_5 (.J(in_1), .clk(j_k_ff_4_q), .K(in_1), .Qn(out_3), .reset(in_2));  // open: Q, preset, en
endmodule

module _093 (
  input  in_1,
  input  in_2,
  output out_3,
  output out_4,
  output out_5,
  output out_6,
  output out_7,
  output out_8
);

  wire and_1_out, and_2_out, clock_1_out, j_k_ff_1_qn, j_k_ff_2_qn, j_k_ff_3_qn, j_k_ff_4_qn, j_k_ff_5_qn,
       not_1_out, not_2_out;

  Clock clock_1 (.out(clock_1_out));
  not not_1 (not_1_out, and_2_out);
  not not_2 (not_2_out, and_1_out);
  and and_1 (and_1_out, in_2, not_1_out);
  and and_2 (and_2_out, ~out_8, out_7, ~out_6, out_5, ~out_4, out_3);  // AND_Gate
  J_K_Flip_Flop j_k_ff_1 (
    .J(in_1), .clk(clock_1_out), .K(in_1), .Q(out_8), .Qn(j_k_ff_1_qn), .reset(not_2_out));  // open: preset, en
  J_K_Flip_Flop j_k_ff_2 (
    .J(in_1), .clk(j_k_ff_1_qn), .K(in_1), .Q(out_7), .Qn(j_k_ff_2_qn), .reset(not_2_out));  // open: preset, en
  J_K_Flip_Flop j_k_ff_3 (
    .J(in_1), .clk(j_k_ff_2_qn), .K(in_1), .Q(out_6), .Qn(j_k_ff_3_qn), .reset(not_2_out));  // open: preset, en
  J_K_Flip_Flop j_k_ff_4 (
    .J(in_1), .clk(j_k_ff_3_qn), .K(in_1), .Q(out_5), .Qn(j_k_ff_4_qn), .reset(not_2_out));  // open: preset, en
  J_K_Flip_Flop j_k_ff_5 (
    .J(in_1), .clk(j_k_ff_4_qn), .K(in_1), .Q(out_4), .Qn(j_k_ff_5_qn), .reset(not_2_out));  // open: preset, en
  J_K_Flip_Flop j_k_ff_6 (.J(in_1), .clk(j_k_ff_5_qn), .K(in_1), .Q(out_3), .reset(not_2_out));  // open: Qn, preset, en
endmodule

module _095 (
  input  in_1,
  output out_2,
  output out_3,
  output out_4,
  output out_5
);

  wire and_1_out, clock_1_out, or_1_out, t_ff_1_qn, t_ff_2_qn, t_ff_3_qn;

  Clock clock_1 (.out(clock_1_out));
  and and_1 (and_1_out, out_5, out_4, out_3, out_2);
  or or_1 (or_1_out, and_1_out, in_1);
  T_Flip_Flop t_ff_1 (
    .clk(clock_1_out), .T(clock_1_out), .Q(out_5), .Qn(t_ff_1_qn), .reset(or_1_out));  // open: preset, en
  T_Flip_Flop t_ff_2 (.clk(t_ff_1_qn), .T(t_ff_1_qn), .Q(out_4), .Qn(t_ff_2_qn), .reset(or_1_out));  // open: preset, en
  T_Flip_Flop t_ff_3 (.clk(t_ff_2_qn), .T(t_ff_2_qn), .Q(out_3), .Qn(t_ff_3_qn), .reset(or_1_out));  // open: preset, en
  T_Flip_Flop t_ff_4 (.clk(t_ff_3_qn), .T(t_ff_3_qn), .Q(out_2), .reset(or_1_out));  // open: Qn, preset, en
endmodule

module _096 (
  input  in_1,
  input  in_2,
  output out_3,
  output out_4,
  output out_5,
  output out_6,
  output out_7,
  output out_8
);

  wire clock_1_out, or_1_out;

  Clock clock_1 (.out(clock_1_out));
  or or_1 (or_1_out, in_1, out_8);
  D_Flip_Flop d_ff_1 (.clk(clock_1_out), .D(or_1_out), .Q(out_3), .reset(in_2));  // open: Qn, preset, en
  D_Flip_Flop d_ff_2 (.clk(clock_1_out), .D(out_3), .Q(out_4), .reset(in_2));  // open: Qn, preset, en
  D_Flip_Flop d_ff_3 (.clk(clock_1_out), .D(out_4), .Q(out_5), .reset(in_2));  // open: Qn, preset, en
  D_Flip_Flop d_ff_4 (.clk(clock_1_out), .D(out_5), .Q(out_6), .reset(in_2));  // open: Qn, preset, en
  D_Flip_Flop d_ff_5 (.clk(clock_1_out), .D(out_6), .Q(out_7), .reset(in_2));  // open: Qn, preset, en
  D_Flip_Flop d_ff_6 (.clk(clock_1_out), .D(out_7), .Q(out_8), .reset(in_2));  // open: Qn, preset, en
endmodule

module _097 (
  input  in_1,
  input  in_2,
  output out_3,
  output out_4,
  output out_5,
  output out_6,
  output out_7,
  output out_8
);

  wire clock_1_out, d_ff_6_qn, or_1_out;

  Clock clock_1 (.out(clock_1_out));
  or or_1 (or_1_out, in_1, d_ff_6_qn);
  D_Flip_Flop d_ff_1 (.clk(clock_1_out), .D(or_1_out), .Q(out_3), .reset(in_2));  // open: Qn, preset, en
  D_Flip_Flop d_ff_2 (.clk(clock_1_out), .D(out_3), .Q(out_4), .reset(in_2));  // open: Qn, preset, en
  D_Flip_Flop d_ff_3 (.clk(clock_1_out), .D(out_4), .Q(out_5), .reset(in_2));  // open: Qn, preset, en
  D_Flip_Flop d_ff_4 (.clk(clock_1_out), .D(out_5), .Q(out_6), .reset(in_2));  // open: Qn, preset, en
  D_Flip_Flop d_ff_5 (.clk(clock_1_out), .D(out_6), .Q(out_7), .reset(in_2));  // open: Qn, preset, en
  D_Flip_Flop d_ff_6 (.clk(clock_1_out), .D(out_7), .Q(out_8), .Qn(d_ff_6_qn), .reset(in_2));  // open: preset, en
endmodule
