// Logisim project Exercicio03.circ as structural Verilog: 1 circuit, main circuit main
module main (
  input  in_1,
  input  in_2,
  input  in_3,
  output out_4,
  output out_5,
  output out_6,
  output out_7,
  output out_8,
  output out_9
);

  wire j_k_ff_1_qn, j_k_ff_2_qn, j_k_ff_3_qn, j_k_ff_4_qn, j_k_ff_5_qn, nand_1_out, nand_2_out, not_1_out,
       not_2_out, not_3_out, not_4_out;

  // Probe on {out_4, out_5, out_6, out_7, out_8, out_9}
  nand nand_1 (nand_1_out, not_1_out, out_8, not_2_out, out_6, not_3_out, not_4_out);
  J_K_Flip_Flop j_k_ff_1 (
    .J(in_1), .clk(in_2), .K(in_1), .Q(out_9), .Qn(j_k_ff_1_qn), .reset(nand_2_out));  // open: preset, en
  nand nand_2 (nand_2_out, in_3, nand_1_out);
  not not_1 (not_1_out, out_9);
  not not_2 (not_2_out, out_7);
  not not_3 (not_3_out, out_5);
  not not_4 (not_4_out, out_4);
  J_K_Flip_Flop j_k_ff_2 (
    .J(in_1), .clk(j_k_ff_1_qn), .K(in_1), .Q(out_8), .Qn(j_k_ff_2_qn), .reset(nand_2_out));  // open: preset, en
  J_K_Flip_Flop j_k_ff_3 (
    .J(in_1), .clk(j_k_ff_2_qn), .K(in_1), .Q(out_7), .Qn(j_k_ff_3_qn), .reset(nand_2_out));  // open: preset, en
  J_K_Flip_Flop j_k_ff_4 (
    .J(in_1), .clk(j_k_ff_3_qn), .K(in_1), .Q(out_6), .Qn(j_k_ff_4_qn), .reset(nand_2_out));  // open: preset, en
  J_K_Flip_Flop j_k_ff_5 (
    .J(in_1), .clk(j_k_ff_4_qn), .K(in_1), .Q(out_5), .Qn(j_k_ff_5_qn), .reset(nand_2_out));  // open: preset, en
  J_K_Flip_Flop j_k_ff_6 (
    .J(in_1), .clk(j_k_ff_5_qn), .K(in_1), .Q(out_4), .reset(nand_2_out));  // open: Qn, preset, en
endmodule
