// Logisim project Circ guia09.circ as structural Verilog
module Exemplo0091 (
  input  _1,
  input  CLR,
  output out_3,
  output out_4,
  output out_5,
  output out_6,
  output out_7
);

  wire clock_1_out;

  Clock clock_1 (.out(clock_1_out));
  J_K_Flip_Flop j_k_ff_1 (.J(_1), .clk(out_4), .K(_1), .Qn(out_3), .reset(CLR));  // open: Q, preset, en
  J_K_Flip_Flop j_k_ff_2 (.J(_1), .clk(out_5), .K(_1), .Qn(out_4), .reset(CLR));  // open: Q, preset, en
  J_K_Flip_Flop j_k_ff_3 (.J(_1), .clk(out_6), .K(_1), .Qn(out_5), .reset(CLR));  // open: Q, preset, en
  J_K_Flip_Flop j_k_ff_4 (.J(_1), .clk(out_7), .K(_1), .Qn(out_6), .reset(CLR));  // open: Q, preset, en
  J_K_Flip_Flop j_k_ff_5 (.J(_1), .clk(clock_1_out), .K(_1), .Qn(out_7), .reset(CLR));  // open: Q, preset, en

  // Notes on the sheet:
  //   Pulse
endmodule

module Exemplo0092 (
  input  _1,
  input  CLR,
  output out_3,
  output out_4,
  output out_5,
  output out_6,
  output out_7
);

  wire clock_1_out, j_k_ff_2_q, j_k_ff_3_q, j_k_ff_4_q, j_k_ff_5_q;

  Clock clock_1 (.out(clock_1_out));
  J_K_Flip_Flop j_k_ff_1 (.J(_1), .clk(j_k_ff_2_q), .K(_1), .Qn(out_3), .reset(CLR));  // open: Q, preset, en
  J_K_Flip_Flop j_k_ff_2 (
    .J(_1), .clk(j_k_ff_3_q), .K(_1), .Q(j_k_ff_2_q), .Qn(out_4), .reset(CLR));  // open: preset, en
  J_K_Flip_Flop j_k_ff_3 (
    .J(_1), .clk(j_k_ff_4_q), .K(_1), .Q(j_k_ff_3_q), .Qn(out_5), .reset(CLR));  // open: preset, en
  J_K_Flip_Flop j_k_ff_4 (
    .J(_1), .clk(j_k_ff_5_q), .K(_1), .Q(j_k_ff_4_q), .Qn(out_6), .reset(CLR));  // open: preset, en
  J_K_Flip_Flop j_k_ff_5 (
    .J(_1), .clk(clock_1_out), .K(_1), .Q(j_k_ff_5_q), .Qn(out_7), .reset(CLR));  // open: preset, en

  // Notes on the sheet:
  //   Pulse
endmodule

module Exemplo0093 (
  input  _1,
  input  CLR,
  output out_3,
  output out_4,
  output out_5,
  output out_6,
  output out_7,
  output out_8
);

  wire and_1_out, and_2_out, clock_1_out, j_k_ff_1_qn, j_k_ff_2_qn, j_k_ff_3_qn, j_k_ff_4_qn, j_k_ff_5_qn,
       not_1_out, not_2_out;

  Clock clock_1 (.out(clock_1_out));
  not not_1 (not_1_out, and_2_out);
  and and_1 (and_1_out, CLR, not_1_out);
  not not_2 (not_2_out, and_1_out);
  and and_2 (and_2_out, ~out_8, out_7, ~out_6, out_5, ~out_4, out_3);  // AND_Gate
  J_K_Flip_Flop j_k_ff_1 (
    .J(_1), .clk(clock_1_out), .K(_1), .Q(out_8), .Qn(j_k_ff_1_qn), .reset(not_2_out));  // open: preset, en
  J_K_Flip_Flop j_k_ff_2 (
    .J(_1), .clk(j_k_ff_1_qn), .K(_1), .Q(out_7), .Qn(j_k_ff_2_qn), .reset(not_2_out));  // open: preset, en
  J_K_Flip_Flop j_k_ff_3 (
    .J(_1), .clk(j_k_ff_2_qn), .K(_1), .Q(out_6), .Qn(j_k_ff_3_qn), .reset(not_2_out));  // open: preset, en
  J_K_Flip_Flop j_k_ff_4 (
    .J(_1), .clk(j_k_ff_3_qn), .K(_1), .Q(out_5), .Qn(j_k_ff_4_qn), .reset(not_2_out));  // open: preset, en
  J_K_Flip_Flop j_k_ff_5 (
    .J(_1), .clk(j_k_ff_4_qn), .K(_1), .Q(out_4), .Qn(j_k_ff_5_qn), .reset(not_2_out));  // open: preset, en
  J_K_Flip_Flop j_k_ff_6 (.J(_1), .clk(j_k_ff_5_qn), .K(_1), .Q(out_3), .reset(not_2_out));  // open: Qn, preset, en

  // Notes on the sheet:
  //   Pulse
endmodule

module Exemplo0094 (
  input  _1,
  input  CLR,
  output out_3,
  output out_4,
  output out_5,
  output out_6,
  output out_7,
  output out_8
);

  wire and_1_out, and_2_out, clock_1_out, j_k_ff_1_qn, j_k_ff_2_qn, j_k_ff_3_qn, j_k_ff_4_qn, j_k_ff_5_qn,
       not_1_out, not_2_out;

  Clock clock_1 (.out(clock_1_out));
  not not_1 (not_1_out, and_2_out);
  not not_2 (not_2_out, and_1_out);
  and and_1 (and_1_out, CLR, not_1_out);
  and and_2 (and_2_out, ~out_8, out_7, ~out_6, out_5, ~out_4, out_3);  // AND_Gate
  J_K_Flip_Flop j_k_ff_1 (
    .J(_1), .clk(clock_1_out), .K(_1), .Q(out_8), .Qn(j_k_ff_1_qn), .reset(not_2_out));  // open: preset, en
  J_K_Flip_Flop j_k_ff_2 (
    .J(_1), .clk(j_k_ff_1_qn), .K(_1), .Q(out_7), .Qn(j_k_ff_2_qn), .reset(not_2_out));  // open: preset, en
  J_K_Flip_Flop j_k_ff_3 (
    .J(_1), .clk(j_k_ff_2_qn), .K(_1), .Q(out_6), .Qn(j_k_ff_3_qn), .reset(not_2_out));  // open: preset, en
  J_K_Flip_Flop j_k_ff_4 (
    .J(_1), .clk(j_k_ff_3_qn), .K(_1), .Q(out_5), .Qn(j_k_ff_4_qn), .reset(not_2_out));  // open: preset, en
  J_K_Flip_Flop j_k_ff_5 (
    .J(_1), .clk(j_k_ff_4_qn), .K(_1), .Q(out_4), .Qn(j_k_ff_5_qn), .reset(not_2_out));  // open: preset, en
  J_K_Flip_Flop j_k_ff_6 (.J(_1), .clk(j_k_ff_5_qn), .K(_1), .Q(out_3), .reset(not_2_out));  // open: Qn, preset, en

  // Notes on the sheet:
  //   Pulse
endmodule

module Exemplo0095 (
  input  Pulse,
  input  CLR,
  output out_3,
  output out_4,
  output out_5,
  output out_6
);

  wire and_1_out, or_1_out, t_ff_2_qn, t_ff_3_qn, t_ff_4_qn;

  or or_1 (or_1_out, CLR, and_1_out);
  and and_1 (and_1_out, out_3, ~out_4, out_5, ~out_6);  // AND_Gate
  T_Flip_Flop t_ff_1 (.clk(t_ff_2_qn), .T(t_ff_2_qn), .Q(out_3), .reset(or_1_out));  // open: Qn, preset, en
  T_Flip_Flop t_ff_2 (.clk(t_ff_3_qn), .T(t_ff_3_qn), .Q(out_4), .Qn(t_ff_2_qn), .reset(or_1_out));  // open: preset, en
  T_Flip_Flop t_ff_3 (.clk(t_ff_4_qn), .T(t_ff_4_qn), .Q(out_5), .Qn(t_ff_3_qn), .reset(or_1_out));  // open: preset, en
  T_Flip_Flop t_ff_4 (.clk(Pulse), .T(Pulse), .Q(out_6), .Qn(t_ff_4_qn), .reset(or_1_out));  // open: preset, en
endmodule

module Exemplo0096 (
  input  Input,
  input  Clear,
  output out_3,
  output out_4,
  output out_5,
  output out_6,
  output out_7,
  output out_8
);

  wire clock_1_out, or_1_out;

  Clock clock_1 (.out(clock_1_out));
  or or_1 (or_1_out, Input, out_3);
  D_Flip_Flop d_ff_1 (.clk(clock_1_out), .D(or_1_out), .Q(out_4), .reset(Clear));  // open: Qn, preset, en
  D_Flip_Flop d_ff_2 (.clk(clock_1_out), .D(out_4), .Q(out_6), .reset(Clear));  // open: Qn, preset, en
  D_Flip_Flop d_ff_3 (.clk(clock_1_out), .D(out_6), .Q(out_8), .reset(Clear));  // open: Qn, preset, en
  D_Flip_Flop d_ff_4 (.clk(clock_1_out), .D(out_8), .Q(out_7), .reset(Clear));  // open: Qn, preset, en
  D_Flip_Flop d_ff_5 (.clk(clock_1_out), .D(out_7), .Q(out_5), .reset(Clear));  // open: Qn, preset, en
  D_Flip_Flop d_ff_6 (.clk(clock_1_out), .D(out_5), .Q(out_3), .reset(Clear));  // open: Qn, preset, en

  // Notes on the sheet:
  //   Clock
endmodule

module Exemplo0097 (
  input  Input,
  input  Clear,
  output out_3,
  output out_4,
  output out_5,
  output out_6,
  output out_7,
  output out_8
);

  wire clock_1_out, d_ff_6_qn, or_1_out;

  Clock clock_1 (.out(clock_1_out));
  or or_1 (or_1_out, Input, d_ff_6_qn);
  D_Flip_Flop d_ff_1 (.clk(clock_1_out), .D(or_1_out), .Q(out_4), .reset(Clear));  // open: Qn, preset, en
  D_Flip_Flop d_ff_2 (.clk(clock_1_out), .D(out_4), .Q(out_6), .reset(Clear));  // open: Qn, preset, en
  D_Flip_Flop d_ff_3 (.clk(clock_1_out), .D(out_6), .Q(out_8), .reset(Clear));  // open: Qn, preset, en
  D_Flip_Flop d_ff_4 (.clk(clock_1_out), .D(out_8), .Q(out_7), .reset(Clear));  // open: Qn, preset, en
  D_Flip_Flop d_ff_5 (.clk(clock_1_out), .D(out_7), .Q(out_5), .reset(Clear));  // open: Qn, preset, en
  D_Flip_Flop d_ff_6 (.clk(clock_1_out), .D(out_5), .Q(out_3), .Qn(d_ff_6_qn), .reset(Clear));  // open: preset, en

  // Notes on the sheet:
  //   Clock
endmodule
