// Logisim project Projeto de circuito do Exemplo0064.circ as structural Verilog: 1 circuit, main circuit Exemplo0064
module Exemplo0064 (
  input  pulse,
  input  _1,
  input  CLR,
  output a,
  output b,
  output c,
  output d,
  output e
);

  J_K_Flip_Flop FFJK_1 (.J(_1), .clk(b), .K(_1), .Qn(a), .reset(CLR));  // open: Q, preset, en
  J_K_Flip_Flop FFJK_2 (.J(_1), .clk(c), .K(_1), .Qn(b), .reset(CLR));  // open: Q, preset, en
  J_K_Flip_Flop FFJK_3 (.J(_1), .clk(d), .K(_1), .Qn(c), .reset(CLR));  // open: Q, preset, en
  J_K_Flip_Flop FFJK_4 (.J(pulse), .clk(e), .K(pulse), .Qn(d), .reset(CLR));  // open: Q, preset, en
  J_K_Flip_Flop FFJK_5 (.J(_1), .clk(pulse), .K(_1), .Qn(e), .reset(CLR));  // open: Q, preset, en

  // Notes on the sheet:
  //   Matrícula: 448662
  //   Nome: Josemar Alves Caetano
endmodule
