// Logisim project Projeto de circuito do Exemplo0065.circ as structural Verilog: 1 circuit, main circuit Exemplo0065
module Exemplo0065 (
  input  pulse,
  input  _1,
  input  CLR,
  output a,
  output b,
  output c,
  output d,
  output e
);

  wire FFJK_2_q, FFJK_3_q, FFJK_4_q, FFJK_5_q;

  J_K_Flip_Flop FFJK_1 (.J(_1), .clk(FFJK_2_q), .K(_1), .Qn(a), .reset(CLR));  // open: Q, preset, en
  J_K_Flip_Flop FFJK_2 (.J(_1), .clk(FFJK_3_q), .K(_1), .Q(FFJK_2_q), .Qn(b), .reset(CLR));  // open: preset, en
  J_K_Flip_Flop FFJK_3 (.J(_1), .clk(FFJK_4_q), .K(_1), .Q(FFJK_3_q), .Qn(c), .reset(CLR));  // open: preset, en
  J_K_Flip_Flop FFJK_4 (.J(_1), .clk(FFJK_5_q), .K(_1), .Q(FFJK_4_q), .Qn(d), .reset(CLR));  // open: preset, en
  J_K_Flip_Flop FFJK_5 (.J(_1), .clk(pulse), .K(_1), .Q(FFJK_5_q), .Qn(e), .reset(CLR));  // open: preset, en

  // Notes on the sheet:
  //   Matrícula: 448662
  //   Nome: Josemar Alves Caetano
endmodule
