// Logisim project Projeto de circuito do Exemplo0066.circ as structural Verilog: 1 circuit, main circuit Exemplo0066
module Exemplo0066 (
  input  _1,
  input  pulse,
  input  CLR,
  output a,
  output b,
  output c,
  output d,
  output e,
  output f
);

  wire FFJK_1_qn, FFJK_2_qn, FFJK_3_qn, FFJK_4_qn, FFJK_5_qn, nand_1_out, nand_2_out, not_1_out, not_2_out,
       not_3_out, not_4_out;

  J_K_Flip_Flop FFJK_1 (.J(_1), .clk(pulse), .K(_1), .Q(f), .Qn(FFJK_1_qn), .reset(nand_1_out));  // open: preset, en
  nand nand_1 (nand_1_out, CLR, nand_2_out);
  not not_1 (not_1_out, f);
  not not_2 (not_2_out, d);
  nand nand_2 (nand_2_out, not_1_out, e, not_2_out, c, not_3_out, not_4_out);
  not not_3 (not_3_out, b);
  not not_4 (not_4_out, a);
  J_K_Flip_Flop FFJK_2 (
    .J(_1), .clk(FFJK_1_qn), .K(_1), .Q(e), .Qn(FFJK_2_qn), .reset(nand_1_out));  // open: preset, en
  J_K_Flip_Flop FFJK_3 (
    .J(_1), .clk(FFJK_2_qn), .K(_1), .Q(d), .Qn(FFJK_3_qn), .reset(nand_1_out));  // open: preset, en
  J_K_Flip_Flop FFJK_4 (
    .J(_1), .clk(FFJK_3_qn), .K(_1), .Q(c), .Qn(FFJK_4_qn), .reset(nand_1_out));  // open: preset, en
  J_K_Flip_Flop FFJK_5 (
    .J(_1), .clk(FFJK_4_qn), .K(_1), .Q(b), .Qn(FFJK_5_qn), .reset(nand_1_out));  // open: preset, en
  J_K_Flip_Flop FFJK_6 (.J(_1), .clk(FFJK_5_qn), .K(_1), .Q(a), .reset(nand_1_out));  // open: Qn, preset, en

  // Notes on the sheet:
  //   Matrícula: 448662
  //   Nome: Josemar Alves Caetano
endmodule
