// Logisim project Projeto de circuito do Exemplo0067.circ as structural Verilog: 1 circuit, main circuit Exemplo0067
module Exemplo0067 (
  input  _1,
  input  pulse,
  output a,
  output b,
  output c,
  output d,
  output e,
  output f
);

  wire and_1_out, FFJK_1_qn, FFJK_2_qn, FFJK_3_qn, FFJK_4_qn, FFJK_5_qn, FFJK_6_qn, not_1_out, not_2_out,
       not_3_out, not_4_out, not_5_out, or_1_out;

  J_K_Flip_Flop FFJK_1 (.J(_1), .clk(pulse), .K(_1), .Q(f), .Qn(FFJK_1_qn), .preset(or_1_out));  // open: en, reset
  not not_1 (not_1_out, _1);
  or or_1 (or_1_out, not_1_out, and_1_out);
  not not_2 (not_2_out, FFJK_1_qn);
  not not_3 (not_3_out, FFJK_3_qn);
  and and_1 (and_1_out, not_2_out, FFJK_2_qn, not_3_out, FFJK_4_qn, not_4_out, not_5_out);
  not not_4 (not_4_out, FFJK_5_qn);
  not not_5 (not_5_out, FFJK_6_qn);
  J_K_Flip_Flop FFJK_2 (.J(_1), .clk(f), .K(_1), .Q(e), .Qn(FFJK_2_qn), .preset(or_1_out));  // open: en, reset
  J_K_Flip_Flop FFJK_3 (.J(_1), .clk(e), .K(_1), .Q(d), .Qn(FFJK_3_qn), .preset(or_1_out));  // open: en, reset
  J_K_Flip_Flop FFJK_4 (.J(_1), .clk(d), .K(_1), .Q(c), .Qn(FFJK_4_qn), .preset(or_1_out));  // open: en, reset
  J_K_Flip_Flop FFJK_5 (.J(_1), .clk(c), .K(_1), .Q(b), .Qn(FFJK_5_qn), .preset(or_1_out));  // open: en, reset
  J_K_Flip_Flop FFJK_6 (.J(_1), .clk(b), .K(_1), .Q(a), .Qn(FFJK_6_qn), .preset(or_1_out));  // open: en, reset

  // Notes on the sheet:
  //   Matrícula: 448662
  //   Nome: Josemar Alves Caetano
endmodule
