// Logisim project Projeto de circuito do Exemplo0068.circ as structural Verilog: 1 circuit, main circuit Exemplo0068
module Exemplo0068 (
  input  pulse,
  input  CLR,
  output a,
  output b,
  output c,
  output d
);

  wire AND_1_out, FFT_2_qn, FFT_3_qn, FFT_4_qn, not_1_out, not_2_out, OR_1_out;

  or OR_1 (OR_1_out, CLR, AND_1_out);
  T_Flip_Flop FFT_1 (.clk(FFT_2_qn), .T(FFT_2_qn), .Q(a), .reset(OR_1_out));  // open: Qn, preset, en
  not not_1 (not_1_out, b);
  and AND_1 (AND_1_out, a, not_1_out, c, not_2_out);
  not not_2 (not_2_out, d);
  T_Flip_Flop FFT_2 (.clk(FFT_3_qn), .T(FFT_3_qn), .Q(b), .Qn(FFT_2_qn), .reset(OR_1_out));  // open: preset, en
  T_Flip_Flop FFT_3 (.clk(FFT_4_qn), .T(FFT_4_qn), .Q(c), .Qn(FFT_3_qn), .reset(OR_1_out));  // open: preset, en
  T_Flip_Flop FFT_4 (.clk(pulse), .T(pulse), .Q(d), .Qn(FFT_4_qn), .reset(OR_1_out));  // open: preset, en

  // Notes on the sheet:
  //   Matrícula: 448662
  //   Nome: Josemar Alves Caetano
endmodule
