// Logisim project Projeto de circuito do Exemplo0069.circ as structural Verilog: 1 circuit, main circuit Exemplo0069
module Exemplo0069 (
  input  \input ,
  input  clear,
  output a,
  output b,
  output c,
  output d,
  output e,
  output f
);

  wire clock_out, or_1_out;

  Clock clock (.out(clock_out));
  or or_1 (or_1_out, f, \input );
  D_Flip_Flop FFD_1 (.clk(clock_out), .D(or_1_out), .Q(a), .reset(clear));  // open: Qn, preset, en
  D_Flip_Flop FFD_2 (.clk(clock_out), .D(a), .Q(b), .reset(clear));  // open: Qn, preset, en
  D_Flip_Flop FFD_3 (.clk(clock_out), .D(b), .Q(c), .reset(clear));  // open: Qn, preset, en
  D_Flip_Flop FFD_4 (.clk(clock_out), .D(c), .Q(d), .reset(clear));  // open: Qn, preset, en
  D_Flip_Flop FFD_5 (.clk(clock_out), .D(d), .Q(e), .reset(clear));  // open: Qn, preset, en
  D_Flip_Flop FFD_6 (.clk(clock_out), .D(e), .Q(f), .reset(clear));  // open: Qn, preset, en

  // Notes on the sheet:
  //   Matrícula: 448662
  //   Nome: Josemar Alves Caetano
endmodule
