// Logisim project testeLogisim.circ as structural Verilog
module Ex_01 (
  input  _1,
  input  pulse,
  input  CLR,
  output a,
  output b,
  output c,
  output d,
  output e
);

  // Probe on {a, b, c, d, e}
  J_K_Flip_Flop j_k_ff_1 (.J(_1), .clk(b), .K(_1), .Qn(a), .reset(CLR));  // open: Q, preset, en
  J_K_Flip_Flop j_k_ff_2 (.J(_1), .clk(c), .K(_1), .Qn(b), .reset(CLR));  // open: Q, preset, en
  J_K_Flip_Flop j_k_ff_3 (.J(_1), .clk(d), .K(_1), .Qn(c), .reset(CLR));  // open: Q, preset, en
  J_K_Flip_Flop j_k_ff_4 (.J(_1), .clk(e), .K(_1), .Qn(d), .reset(CLR));  // open: Q, preset, en
  J_K_Flip_Flop j_k_ff_5 (.J(_1), .clk(pulse), .K(_1), .Qn(e), .reset(CLR));  // open: Q, preset, en
endmodule

module EX_02 (
  input  Pulse,
  input  _1,
  input  CLR,
  output a,
  output b,
  output c,
  output d,
  output e
);

  wire j_k_ff_2_q, j_k_ff_3_q, j_k_ff_4_q, j_k_ff_5_q;

  // Probe on {a, b, c, d, e}
  J_K_Flip_Flop j_k_ff_1 (.J(_1), .clk(j_k_ff_2_q), .K(_1), .Qn(a), .reset(CLR));  // open: Q, preset, en
  J_K_Flip_Flop j_k_ff_2 (.J(_1), .clk(j_k_ff_3_q), .K(_1), .Q(j_k_ff_2_q), .Qn(b), .reset(CLR));  // open: preset, en
  J_K_Flip_Flop j_k_ff_3 (.J(_1), .clk(j_k_ff_4_q), .K(_1), .Q(j_k_ff_3_q), .Qn(c), .reset(CLR));  // open: preset, en
  J_K_Flip_Flop j_k_ff_4 (.J(_1), .clk(j_k_ff_5_q), .K(_1), .Q(j_k_ff_4_q), .Qn(d), .reset(CLR));  // open: preset, en
  J_K_Flip_Flop j_k_ff_5 (.J(_1), .clk(Pulse), .K(_1), .Q(j_k_ff_5_q), .Qn(e), .reset(CLR));  // open: preset, en
endmodule

module EX_03 (
  input  pulse,
  input  _1,
  input  CLR,
  output a,
  output b,
  output c,
  output d,
  output e,
  output f
);

  wire and_1_out, j_k_ff_1_qn, j_k_ff_2_qn, j_k_ff_3_qn, j_k_ff_4_qn, j_k_ff_5_qn, j_k_ff_6_qn, or_1_out;

  // Probe on {a, b, c, d, e, f}
  and and_1 (and_1_out, j_k_ff_1_qn, e, j_k_ff_3_qn, c, j_k_ff_5_qn, j_k_ff_6_qn);
  J_K_Flip_Flop j_k_ff_1 (.J(_1), .clk(pulse), .K(_1), .Q(f), .Qn(j_k_ff_1_qn), .reset(or_1_out));  // open: preset, en
  or or_1 (or_1_out, CLR, and_1_out);
  J_K_Flip_Flop j_k_ff_2 (
    .J(_1), .clk(j_k_ff_1_qn), .K(_1), .Q(e), .Qn(j_k_ff_2_qn), .reset(or_1_out));  // open: preset, en
  J_K_Flip_Flop j_k_ff_3 (
    .J(_1), .clk(j_k_ff_2_qn), .K(_1), .Q(d), .Qn(j_k_ff_3_qn), .reset(or_1_out));  // open: preset, en
  J_K_Flip_Flop j_k_ff_4 (
    .J(_1), .clk(j_k_ff_3_qn), .K(_1), .Q(c), .Qn(j_k_ff_4_qn), .reset(or_1_out));  // open: preset, en
  J_K_Flip_Flop j_k_ff_5 (
    .J(_1), .clk(j_k_ff_4_qn), .K(_1), .Q(b), .Qn(j_k_ff_5_qn), .reset(or_1_out));  // open: preset, en
  J_K_Flip_Flop j_k_ff_6 (
    .J(_1), .clk(j_k_ff_5_qn), .K(_1), .Q(a), .Qn(j_k_ff_6_qn), .reset(or_1_out));  // open: preset, en
endmodule

module EX_04 (
  input  pulse,
  input  CLR,
  output a,
  output b,
  output c,
  output d,
  output e,
  output f
);

  wire and_1_out, j_k_ff_1_qn, j_k_ff_2_qn, j_k_ff_3_qn, j_k_ff_4_qn, j_k_ff_5_qn, j_k_ff_6_qn, or_1_out;

  // Probe on {a, b, c, d, e, f}
  and and_1 (and_1_out, j_k_ff_1_qn, j_k_ff_2_qn, c, j_k_ff_4_qn, e, j_k_ff_6_qn);
  J_K_Flip_Flop j_k_ff_1 (
    .J(j_k_ff_2_qn), .clk(j_k_ff_2_qn), .K(j_k_ff_2_qn), .Q(a), .Qn(j_k_ff_1_qn), .reset(or_1_out));  // open: preset, en
  or or_1 (or_1_out, CLR, and_1_out);
  J_K_Flip_Flop j_k_ff_2 (
    .J(j_k_ff_3_qn), .clk(j_k_ff_3_qn), .K(j_k_ff_3_qn), .Q(b), .Qn(j_k_ff_2_qn), .reset(or_1_out));  // open: preset, en
  J_K_Flip_Flop j_k_ff_3 (
    .J(j_k_ff_4_qn), .clk(j_k_ff_4_qn), .K(j_k_ff_4_qn), .Q(c), .Qn(j_k_ff_3_qn), .reset(or_1_out));  // open: preset, en
  J_K_Flip_Flop j_k_ff_4 (
    .J(j_k_ff_5_qn), .clk(j_k_ff_5_qn), .K(j_k_ff_5_qn), .Q(d), .Qn(j_k_ff_4_qn), .reset(or_1_out));  // open: preset, en
  J_K_Flip_Flop j_k_ff_5 (
    .J(j_k_ff_6_qn), .clk(j_k_ff_6_qn), .K(j_k_ff_6_qn), .Q(e), .Qn(j_k_ff_5_qn), .reset(or_1_out));  // open: preset, en
  J_K_Flip_Flop j_k_ff_6 (
    .J(pulse), .clk(pulse), .K(pulse), .Q(f), .Qn(j_k_ff_6_qn), .reset(or_1_out));  // open: preset, en
endmodule

module EX_05 (
  input  pulso,
  input  clear,
  output a,
  output b,
  output c,
  output d
);

  wire and_1_out, or_1_out, t_ff_2_qn, t_ff_3_qn, t_ff_4_qn;

  // Probe on {a, b, c, d}
  T_Flip_Flop t_ff_1 (.clk(t_ff_2_qn), .T(t_ff_2_qn), .Q(a), .reset(or_1_out));  // open: Qn, preset, en
  or or_1 (or_1_out, clear, and_1_out);
  and and_1 (and_1_out, a, t_ff_2_qn, c, t_ff_4_qn);
  T_Flip_Flop t_ff_2 (.clk(t_ff_3_qn), .T(t_ff_3_qn), .Q(b), .Qn(t_ff_2_qn), .reset(or_1_out));  // open: preset, en
  T_Flip_Flop t_ff_3 (.clk(t_ff_4_qn), .T(t_ff_4_qn), .Q(c), .Qn(t_ff_3_qn), .reset(or_1_out));  // open: preset, en
  T_Flip_Flop t_ff_4 (.clk(pulso), .T(pulso), .Q(d), .Qn(t_ff_4_qn), .reset(or_1_out));  // open: preset, en
endmodule

module EX_06 (
  input  in,
  input  CLR,
  output a,
  output b,
  output c,
  output d,
  output e,
  output f
);

  wire clock_1_out, j_k_ff_1_qn, j_k_ff_2_qn, j_k_ff_3_qn, j_k_ff_4_qn, j_k_ff_5_qn, not_1_out, or_1_out;

  Clock clock_1 (.out(clock_1_out));
  or or_1 (or_1_out, in, f);
  not not_1 (not_1_out, or_1_out);
  J_K_Flip_Flop j_k_ff_1 (
    .J(or_1_out), .clk(clock_1_out), .K(not_1_out), .Q(a), .Qn(j_k_ff_1_qn), .reset(CLR));  // open: preset, en
  J_K_Flip_Flop j_k_ff_2 (
    .J(a), .clk(clock_1_out), .K(j_k_ff_1_qn), .Q(b), .Qn(j_k_ff_2_qn), .reset(CLR));  // open: preset, en
  J_K_Flip_Flop j_k_ff_3 (
    .J(b), .clk(clock_1_out), .K(j_k_ff_2_qn), .Q(c), .Qn(j_k_ff_3_qn), .reset(CLR));  // open: preset, en
  J_K_Flip_Flop j_k_ff_4 (
    .J(c), .clk(clock_1_out), .K(j_k_ff_3_qn), .Q(d), .Qn(j_k_ff_4_qn), .reset(CLR));  // open: preset, en
  J_K_Flip_Flop j_k_ff_5 (
    .J(d), .clk(clock_1_out), .K(j_k_ff_4_qn), .Q(e), .Qn(j_k_ff_5_qn), .reset(CLR));  // open: preset, en
  J_K_Flip_Flop j_k_ff_6 (.J(e), .clk(clock_1_out), .K(j_k_ff_5_qn), .Q(f), .reset(CLR));  // open: Qn, preset, en

  // Notes on the sheet:
  //   CLK
endmodule

module EX_07 (
  input  in,
  input  CLR,
  output a,
  output b,
  output c,
  output d,
  output e,
  output f
);

  wire clock_1_out, j_k_ff_2_qn, j_k_ff_3_qn, j_k_ff_4_qn, j_k_ff_5_qn, j_k_ff_6_qn, not_1_out, or_1_out;

  Clock clock_1 (.out(clock_1_out));
  or or_1 (or_1_out, in, a);
  J_K_Flip_Flop j_k_ff_1 (.J(b), .clk(clock_1_out), .K(j_k_ff_2_qn), .Q(a), .reset(CLR));  // open: Qn, preset, en
  J_K_Flip_Flop j_k_ff_2 (
    .J(c), .clk(clock_1_out), .K(j_k_ff_3_qn), .Q(b), .Qn(j_k_ff_2_qn));  // open: preset, en, reset
  J_K_Flip_Flop j_k_ff_3 (
    .J(d), .clk(clock_1_out), .K(j_k_ff_4_qn), .Q(c), .Qn(j_k_ff_3_qn), .reset(CLR));  // open: preset, en
  J_K_Flip_Flop j_k_ff_4 (
    .J(e), .clk(clock_1_out), .K(j_k_ff_5_qn), .Q(d), .Qn(j_k_ff_4_qn), .reset(CLR));  // open: preset, en
  J_K_Flip_Flop j_k_ff_5 (
    .J(f), .clk(clock_1_out), .K(j_k_ff_6_qn), .Q(e), .Qn(j_k_ff_5_qn), .reset(CLR));  // open: preset, en
  not not_1 (not_1_out, or_1_out);
  J_K_Flip_Flop j_k_ff_6 (
    .J(or_1_out), .clk(clock_1_out), .K(not_1_out), .Q(f), .Qn(j_k_ff_6_qn), .reset(CLR));  // open: preset, en

  // Notes on the sheet:
  //   CLK
endmodule
