// Logisim project contador_assincrono_crescente.circ as structural Verilog: 1 circuit, main circuit cont assinc crescente
module cont_assinc_crescente (
  input  Pulse,
  input  CLR,
  output out_3,
  output out_4,
  output out_5,
  output out_6,
  output out_7
);

  wire j_k_ff_2_qn, j_k_ff_3_qn, j_k_ff_4_qn, j_k_ff_5_qn;

  J_K_Flip_Flop j_k_ff_1 (.J(1'b1), .clk(j_k_ff_2_qn), .K(1'b1), .Q(out_3), .reset(CLR));  // open: Qn, preset, en
  J_K_Flip_Flop j_k_ff_2 (
    .J(1'b1), .clk(j_k_ff_3_qn), .K(1'b1), .Q(out_4), .Qn(j_k_ff_2_qn), .reset(CLR));  // open: preset, en
  J_K_Flip_Flop j_k_ff_3 (
    .J(1'b1), .clk(j_k_ff_4_qn), .K(1'b1), .Q(out_5), .Qn(j_k_ff_3_qn), .reset(CLR));  // open: preset, en
  J_K_Flip_Flop j_k_ff_4 (
    .J(1'b1), .clk(j_k_ff_5_qn), .K(1'b1), .Q(out_6), .Qn(j_k_ff_4_qn), .reset(CLR));  // open: preset, en
  J_K_Flip_Flop j_k_ff_5 (
    .J(1'b1), .clk(Pulse), .K(1'b1), .Q(out_7), .Qn(j_k_ff_5_qn), .reset(CLR));  // open: preset, en

  // Notes on the sheet:
  //   Contador Assíncrono Crescente
  //   Ana Cristina - 427385
endmodule
