// Logisim project contador_assincrono_decrescente.circ as structural Verilog: 1 circuit, main circuit cont assinc descrescente
module cont_assinc_descrescente (
  input  Pulso,
  input  CLR,
  output out_3,
  output out_4,
  output out_5,
  output out_6,
  output out_7
);

  J_K_Flip_Flop j_k_ff_1 (.J(1'b1), .clk(out_4), .K(1'b1), .Q(out_3), .reset(CLR));  // open: Qn, preset, en
  J_K_Flip_Flop j_k_ff_2 (.J(1'b1), .clk(out_5), .K(1'b1), .Q(out_4), .reset(CLR));  // open: Qn, preset, en
  J_K_Flip_Flop j_k_ff_3 (.J(1'b1), .clk(out_6), .K(1'b1), .Q(out_5), .reset(CLR));  // open: Qn, preset, en
  J_K_Flip_Flop j_k_ff_4 (.J(1'b1), .clk(out_7), .K(1'b1), .Q(out_6), .reset(CLR));  // open: Qn, preset, en
  J_K_Flip_Flop j_k_ff_5 (.J(1'b1), .clk(Pulso), .K(1'b1), .Q(out_7), .reset(CLR));  // open: Qn, preset, en

  // Notes on the sheet:
  //   Contadro Assíncrono Descrescente
  //   Ana Cristina - 427385
endmodule
