// Logisim project contador_decadico_crescente.circ as structural Verilog: 1 circuit, main circuit cont dec crescente
module cont_dec_crescente (
  input  Pulse,
  input  CLR,
  output out_3,
  output out_4,
  output out_5,
  output out_6,
  output out_7
);

  wire j_k_ff_1_qn, j_k_ff_2_qn, j_k_ff_3_qn, j_k_ff_4_qn, nand_1_out, nand_2_out, not_1_out, not_2_out,
       not_3_out;

  nand nand_1 (nand_1_out, not_1_out, out_6, not_2_out, out_4, not_3_out);
  nand nand_2 (nand_2_out, CLR, nand_1_out);
  not not_1 (not_1_out, out_7);
  not not_2 (not_2_out, out_5);
  not not_3 (not_3_out, out_3);
  J_K_Flip_Flop j_k_ff_1 (
    .J(1'b1), .clk(Pulse), .K(1'b1), .Q(out_7), .Qn(j_k_ff_1_qn), .reset(nand_2_out));  // open: preset, en
  J_K_Flip_Flop j_k_ff_2 (
    .J(1'b1), .clk(j_k_ff_1_qn), .K(1'b1), .Q(out_6), .Qn(j_k_ff_2_qn), .reset(nand_2_out));  // open: preset, en
  J_K_Flip_Flop j_k_ff_3 (
    .J(1'b1), .clk(j_k_ff_2_qn), .K(1'b1), .Q(out_5), .Qn(j_k_ff_3_qn), .reset(nand_2_out));  // open: preset, en
  J_K_Flip_Flop j_k_ff_4 (
    .J(1'b1), .clk(j_k_ff_3_qn), .K(1'b1), .Q(out_4), .Qn(j_k_ff_4_qn), .reset(nand_2_out));  // open: preset, en
  J_K_Flip_Flop j_k_ff_5 (
    .J(1'b1), .clk(j_k_ff_4_qn), .K(1'b1), .Q(out_3), .reset(nand_2_out));  // open: Qn, preset, en

  // Notes on the sheet:
  //   Contador Decádico Crescente
  //   Ana Cristina - 427385
endmodule
