// Logisim project contador_decadico_decrescente.circ as structural Verilog: 1 circuit, main circuit cont dec descrescente
module cont_dec_descrescente (
  input  Pulse,
  input  CLR,
  output a,
  output b,
  output c,
  output d,
  output e
);

  wire and_1_out, j_k_ff_1_qn, j_k_ff_2_qn, j_k_ff_3_qn, j_k_ff_4_qn, j_k_ff_5_qn, not_1_out, not_2_out,
       not_3_out, or_1_out;

  not not_1 (not_1_out, 1'b1);
  or or_1 (or_1_out, not_1_out, and_1_out);
  not not_2 (not_2_out, j_k_ff_1_qn);
  not not_3 (not_3_out, j_k_ff_3_qn);
  and and_1 (and_1_out, not_2_out, j_k_ff_2_qn, not_3_out, j_k_ff_4_qn, j_k_ff_5_qn);
  J_K_Flip_Flop j_k_ff_1 (
    .J(1'b1), .clk(Pulse), .K(1'b1), .Q(e), .Qn(j_k_ff_1_qn), .preset(or_1_out), .reset(CLR));  // open: en
  J_K_Flip_Flop j_k_ff_2 (
    .J(1'b1), .clk(e), .K(1'b1), .Q(d), .Qn(j_k_ff_2_qn), .preset(or_1_out), .reset(CLR));  // open: en
  J_K_Flip_Flop j_k_ff_3 (
    .J(1'b1), .clk(d), .K(1'b1), .Q(c), .Qn(j_k_ff_3_qn), .preset(or_1_out), .reset(CLR));  // open: en
  J_K_Flip_Flop j_k_ff_4 (
    .J(1'b1), .clk(c), .K(1'b1), .Q(b), .Qn(j_k_ff_4_qn), .preset(or_1_out), .reset(CLR));  // open: en
  J_K_Flip_Flop j_k_ff_5 (
    .J(1'b1), .clk(b), .K(1'b1), .Q(a), .Qn(j_k_ff_5_qn), .preset(or_1_out), .reset(CLR));  // open: en

  // Notes on the sheet:
  //   Contador Decádico Decrescente
  //   Ana Cristina - 427385
endmodule
