// Logisim project contador_modulo_oito.circ as structural Verilog: 1 circuit, main circuit cont mod 8
module cont_mod_8 (
  input  Pulse,
  input  CLR,
  output a,
  output b,
  output c,
  output d
);

  wire and_1_out, not_1_out, not_2_out, not_3_out, or_1_out, t_ff_2_qn, t_ff_3_qn, t_ff_4_qn;

  or or_1 (or_1_out, CLR, and_1_out);
  and and_1 (and_1_out, a, not_1_out, not_2_out, not_3_out);
  T_Flip_Flop t_ff_1 (.clk(t_ff_2_qn), .T(t_ff_2_qn), .Q(a), .reset(or_1_out));  // open: Qn, preset, en
  not not_1 (not_1_out, b);
  not not_2 (not_2_out, c);
  not not_3 (not_3_out, d);
  T_Flip_Flop t_ff_2 (.clk(t_ff_3_qn), .T(t_ff_3_qn), .Q(b), .Qn(t_ff_2_qn), .reset(or_1_out));  // open: preset, en
  T_Flip_Flop t_ff_3 (.clk(t_ff_4_qn), .T(t_ff_4_qn), .Q(c), .Qn(t_ff_3_qn), .reset(or_1_out));  // open: preset, en
  T_Flip_Flop t_ff_4 (.clk(Pulse), .T(Pulse), .Q(d), .Qn(t_ff_4_qn), .reset(or_1_out));  // open: preset, en

  // Notes on the sheet:
  //   Contador Módulo 8
  //   Ana Cristina - 427385
endmodule
