// Logisim project guia9.circ as structural Verilog: 5 circuits, main circuit main
module main (
  input  in_1,
  input  in_2,
  input  in_3,
  input  in_4,
  output out_5,
  output out_6
);

  J_K_Flip_Flop j_k_ff_1 (.J(in_2), .clk(in_1), .K(in_3), .Q(out_5), .Qn(out_6), .reset(in_4));  // open: preset, en
endmodule

module decre (
  input  in_1,
  input  in_2,
  input  in_3,
  output out_4,
  output out_5,
  output out_6,
  output out_7,
  output out_8
);

  J_K_Flip_Flop j_k_ff_1 (.J(in_2), .clk(out_5), .K(in_2), .Qn(out_4), .reset(in_3));  // open: Q, preset, en
  J_K_Flip_Flop j_k_ff_2 (.J(in_2), .clk(out_8), .K(in_2), .Qn(out_5), .reset(in_3));  // open: Q, preset, en
  J_K_Flip_Flop j_k_ff_3 (.J(in_2), .clk(out_6), .K(in_2), .Qn(out_8), .reset(in_3));  // open: Q, preset, en
  J_K_Flip_Flop j_k_ff_4 (.J(in_2), .clk(out_7), .K(in_2), .Qn(out_6), .reset(in_3));  // open: Q, preset, en
  J_K_Flip_Flop j_k_ff_5 (.J(in_2), .clk(in_1), .K(in_2), .Qn(out_7), .reset(in_3));  // open: Q, preset, en
endmodule

module creci (
  input  in_1,
  input  in_2,
  input  in_3,
  output out_4,
  output out_5,
  output out_6,
  output out_7,
  output out_8
);

  wire j_k_ff_2_q, j_k_ff_3_q, j_k_ff_4_q, j_k_ff_5_q;

  J_K_Flip_Flop j_k_ff_1 (.J(in_2), .clk(j_k_ff_2_q), .K(in_2), .Qn(out_4), .reset(in_3));  // open: Q, preset, en
  J_K_Flip_Flop j_k_ff_2 (
    .J(in_2), .clk(j_k_ff_3_q), .K(in_2), .Q(j_k_ff_2_q), .Qn(out_5), .reset(in_3));  // open: preset, en
  J_K_Flip_Flop j_k_ff_3 (
    .J(in_2), .clk(j_k_ff_4_q), .K(in_2), .Q(j_k_ff_3_q), .Qn(out_8), .reset(in_3));  // open: preset, en
  J_K_Flip_Flop j_k_ff_4 (
    .J(in_2), .clk(j_k_ff_5_q), .K(in_2), .Q(j_k_ff_4_q), .Qn(out_6), .reset(in_3));  // open: preset, en
  J_K_Flip_Flop j_k_ff_5 (
    .J(in_2), .clk(in_1), .K(in_2), .Q(j_k_ff_5_q), .Qn(out_7), .reset(in_3));  // open: preset, en
endmodule

module cremodulo10 (
  input  in_1,
  input  in_2,
  input  in_3,
  output out_4,
  output out_5,
  output out_6,
  output out_7,
  output out_8,
  output out_9
);

  wire j_k_ff_1_qn, j_k_ff_2_qn, j_k_ff_3_qn, j_k_ff_4_qn, j_k_ff_5_qn, nand_1_out, nand_2_out, not_1_out,
       not_2_out, not_3_out, not_4_out;

  nand nand_1 (nand_1_out, not_1_out, out_8, not_2_out, out_5, not_3_out, not_4_out);
  not not_1 (not_1_out, out_9);
  not not_2 (not_2_out, out_6);
  not not_3 (not_3_out, out_4);
  not not_4 (not_4_out, out_7);
  J_K_Flip_Flop j_k_ff_1 (
    .J(in_2), .clk(in_1), .K(in_2), .Q(out_9), .Qn(j_k_ff_1_qn), .reset(nand_2_out));  // open: preset, en
  nand nand_2 (nand_2_out, in_3, nand_1_out);
  J_K_Flip_Flop j_k_ff_2 (
    .J(in_2), .clk(j_k_ff_1_qn), .K(in_2), .Q(out_8), .Qn(j_k_ff_2_qn), .reset(nand_2_out));  // open: preset, en
  J_K_Flip_Flop j_k_ff_3 (
    .J(in_2), .clk(j_k_ff_2_qn), .K(in_2), .Q(out_6), .Qn(j_k_ff_3_qn), .reset(nand_2_out));  // open: preset, en
  J_K_Flip_Flop j_k_ff_4 (
    .J(in_2), .clk(j_k_ff_3_qn), .K(in_2), .Q(out_5), .Qn(j_k_ff_4_qn), .reset(nand_2_out));  // open: preset, en
  J_K_Flip_Flop j_k_ff_5 (
    .J(in_2), .clk(j_k_ff_4_qn), .K(in_2), .Q(out_4), .Qn(j_k_ff_5_qn), .reset(nand_2_out));  // open: preset, en
  J_K_Flip_Flop j_k_ff_6 (
    .J(in_2), .clk(j_k_ff_5_qn), .K(in_2), .Q(out_7), .reset(nand_2_out));  // open: Qn, preset, en
endmodule

module contadormodulo10T (
  input  in_1,
  input  in_2,
  output out_3,
  output out_4,
  output out_5,
  output out_6
);

  wire and_1_out, not_1_out, not_2_out, or_1_out, t_ff_2_qn, t_ff_3_qn, t_ff_4_qn;

  or or_1 (or_1_out, in_2, and_1_out);
  not not_1 (not_1_out, out_4);
  and and_1 (and_1_out, out_6, not_1_out, out_5, not_2_out);
  T_Flip_Flop t_ff_1 (.clk(t_ff_2_qn), .T(t_ff_2_qn), .Q(out_6), .reset(or_1_out));  // open: Qn, preset, en
  not not_2 (not_2_out, out_3);
  T_Flip_Flop t_ff_2 (.clk(t_ff_3_qn), .T(t_ff_3_qn), .Q(out_4), .Qn(t_ff_2_qn), .reset(or_1_out));  // open: preset, en
  T_Flip_Flop t_ff_3 (.clk(t_ff_4_qn), .T(t_ff_4_qn), .Q(out_5), .Qn(t_ff_3_qn), .reset(or_1_out));  // open: preset, en
  T_Flip_Flop t_ff_4 (.clk(in_1), .T(in_1), .Q(out_3), .Qn(t_ff_4_qn), .reset(or_1_out));  // open: preset, en
endmodule
