// Logisim project Guia09 - Exercicio04.circ as structural Verilog: 1 circuit, main circuit main
module main (
  input  PULSE,
  input  _1,
  input  CLR,
  output a,
  output b,
  output c,
  output d,
  output e,
  output f
);

  wire j_k_ff_1_qn, j_k_ff_2_qn, j_k_ff_3_qn, j_k_ff_4_qn, j_k_ff_5_qn, j_k_ff_6_qn, nand_1_out, nand_2_out;

  nand nand_1 (nand_1_out, j_k_ff_1_qn, e, j_k_ff_3_qn, c, j_k_ff_5_qn, j_k_ff_6_qn);
  J_K_Flip_Flop j_k_ff_1 (
    .J(_1), .clk(PULSE), .K(_1), .Q(f), .Qn(j_k_ff_1_qn), .reset(nand_2_out));  // open: preset, en
  nand nand_2 (nand_2_out, CLR, nand_1_out);
  J_K_Flip_Flop j_k_ff_2 (
    .J(_1), .clk(j_k_ff_1_qn), .K(_1), .Q(e), .Qn(j_k_ff_2_qn), .reset(nand_2_out));  // open: preset, en
  J_K_Flip_Flop j_k_ff_3 (
    .J(_1), .clk(j_k_ff_2_qn), .K(_1), .Q(d), .Qn(j_k_ff_3_qn), .reset(nand_2_out));  // open: preset, en
  J_K_Flip_Flop j_k_ff_4 (
    .J(_1), .clk(j_k_ff_3_qn), .K(_1), .Q(c), .Qn(j_k_ff_4_qn), .reset(nand_2_out));  // open: preset, en
  J_K_Flip_Flop j_k_ff_5 (
    .J(_1), .clk(j_k_ff_4_qn), .K(_1), .Q(b), .Qn(j_k_ff_5_qn), .reset(nand_2_out));  // open: preset, en
  J_K_Flip_Flop j_k_ff_6 (
    .J(_1), .clk(j_k_ff_5_qn), .K(_1), .Q(a), .Qn(j_k_ff_6_qn), .reset(nand_2_out));  // open: preset, en
endmodule
