// Logisim project Guia09 - Exercicio05.circ as structural Verilog: 1 circuit, main circuit main
module main (
  input  pulso,
  input  CLR,
  output d,
  output c,
  output b,
  output a
);

  wire and_1_out, not_1_out, not_2_out, or_1_out, t_ff_2_qn, t_ff_3_qn, t_ff_4_qn;

  or or_1 (or_1_out, CLR, and_1_out);
  and and_1 (and_1_out, d, not_1_out, b, not_2_out);
  T_Flip_Flop t_ff_1 (.clk(t_ff_2_qn), .T(t_ff_2_qn), .Q(d), .reset(or_1_out));  // open: Qn, preset, en
  not not_1 (not_1_out, c);
  not not_2 (not_2_out, a);
  T_Flip_Flop t_ff_2 (.clk(t_ff_3_qn), .T(t_ff_3_qn), .Q(c), .Qn(t_ff_2_qn), .reset(or_1_out));  // open: preset, en
  T_Flip_Flop t_ff_3 (.clk(t_ff_4_qn), .T(t_ff_4_qn), .Q(b), .Qn(t_ff_3_qn), .reset(or_1_out));  // open: preset, en
  T_Flip_Flop t_ff_4 (.clk(pulso), .T(pulso), .Q(a), .Qn(t_ff_4_qn), .reset(or_1_out));  // open: preset, en
endmodule
