// Logisim project circuitos.circ as structural Verilog: 6 circuits, main circuit main
module main (
);


  // Notes on the sheet:
  //   Isabel Bicalho Amaro
  //   Matricula: 451580
endmodule

module Questao1 (
  input  pulse,
  input  clear,
  output a,
  output b,
  output c,
  output d,
  output e
);

  J_K_Flip_Flop j_k_ff_1 (.J(1'b1), .clk(b), .K(1'b1), .Qn(a), .reset(clear));  // open: Q, preset, en
  J_K_Flip_Flop j_k_ff_2 (.J(1'b1), .clk(c), .K(1'b1), .Qn(b), .reset(clear));  // open: Q, preset, en
  J_K_Flip_Flop j_k_ff_3 (.J(1'b1), .clk(d), .K(1'b1), .Qn(c), .reset(clear));  // open: Q, preset, en
  J_K_Flip_Flop j_k_ff_4 (.J(1'b1), .clk(e), .K(1'b1), .Qn(d), .reset(clear));  // open: Q, preset, en
  J_K_Flip_Flop j_k_ff_5 (.J(1'b1), .clk(pulse), .K(1'b1), .Qn(e), .reset(clear));  // open: Q, preset, en

  // Notes on the sheet:
  //   Isabel Bicalho Amaro
  //   Matricula: 451580
endmodule

module Questao_2 (
  input  pulse,
  input  clear,
  output a,
  output b,
  output c,
  output d,
  output e
);

  wire j_k_ff_2_q, j_k_ff_3_q, j_k_ff_4_q, j_k_ff_5_q;

  J_K_Flip_Flop j_k_ff_1 (.J(1'b1), .clk(j_k_ff_2_q), .K(1'b1), .Qn(a), .reset(clear));  // open: Q, preset, en
  J_K_Flip_Flop j_k_ff_2 (
    .J(1'b1), .clk(j_k_ff_3_q), .K(1'b1), .Q(j_k_ff_2_q), .Qn(b), .reset(clear));  // open: preset, en
  J_K_Flip_Flop j_k_ff_3 (
    .J(1'b1), .clk(j_k_ff_4_q), .K(1'b1), .Q(j_k_ff_3_q), .Qn(c), .reset(clear));  // open: preset, en
  J_K_Flip_Flop j_k_ff_4 (
    .J(1'b1), .clk(j_k_ff_5_q), .K(1'b1), .Q(j_k_ff_4_q), .Qn(d), .reset(clear));  // open: preset, en
  J_K_Flip_Flop j_k_ff_5 (.J(1'b1), .clk(pulse), .K(1'b1), .Q(j_k_ff_5_q), .Qn(e), .reset(clear));  // open: preset, en

  // Notes on the sheet:
  //   Isabel Bicalho Amaro
  //   Matricula: 451580
endmodule

module Questao3 (
  input  pulse,
  input  clear,
  output a,
  output b,
  output c,
  output d,
  output e,
  output f
);

  wire j_k_ff_1_qn, j_k_ff_2_qn, j_k_ff_3_qn, j_k_ff_4_qn, j_k_ff_5_qn, nand_1_out, nand_2_out, not_1_out,
       not_2_out, not_3_out, not_4_out;

  nand nand_1 (nand_1_out, clear, nand_2_out);
  nand nand_2 (nand_2_out, not_1_out, e, not_2_out, c, not_3_out, not_4_out);
  J_K_Flip_Flop j_k_ff_1 (
    .J(1'b1), .clk(pulse), .K(1'b1), .Q(f), .Qn(j_k_ff_1_qn), .reset(nand_1_out));  // open: preset, en
  not not_1 (not_1_out, f);
  not not_2 (not_2_out, d);
  not not_3 (not_3_out, b);
  not not_4 (not_4_out, a);
  J_K_Flip_Flop j_k_ff_2 (
    .J(1'b1), .clk(j_k_ff_1_qn), .K(1'b1), .Q(e), .Qn(j_k_ff_2_qn), .reset(nand_1_out));  // open: preset, en
  J_K_Flip_Flop j_k_ff_3 (
    .J(1'b1), .clk(j_k_ff_2_qn), .K(1'b1), .Q(d), .Qn(j_k_ff_3_qn), .reset(nand_1_out));  // open: preset, en
  J_K_Flip_Flop j_k_ff_4 (
    .J(1'b1), .clk(j_k_ff_3_qn), .K(1'b1), .Q(c), .Qn(j_k_ff_4_qn), .reset(nand_1_out));  // open: preset, en
  J_K_Flip_Flop j_k_ff_5 (
    .J(1'b1), .clk(j_k_ff_4_qn), .K(1'b1), .Q(b), .Qn(j_k_ff_5_qn), .reset(nand_1_out));  // open: preset, en
  J_K_Flip_Flop j_k_ff_6 (.J(1'b1), .clk(j_k_ff_5_qn), .K(1'b1), .Q(a), .reset(nand_1_out));  // open: Qn, preset, en

  // Notes on the sheet:
  //   Matricula: 451580
  //   Isabel Bicalho Amaro
endmodule

module Questao4 (
  input  pulse,
  input  clr,
  output a,
  output b,
  output c,
  output d,
  output e,
  output f
);

  wire and_1_out, j_k_ff_1_qn, j_k_ff_2_qn, j_k_ff_3_qn, j_k_ff_4_qn, j_k_ff_5_qn, j_k_ff_6_qn, not_1_out,
       not_2_out, not_3_out, not_4_out;

  and and_1 (and_1_out, not_1_out, j_k_ff_2_qn, not_2_out, j_k_ff_4_qn, not_3_out, not_4_out);
  J_K_Flip_Flop j_k_ff_1 (
    .J(1'b1), .clk(pulse), .K(1'b1), .Q(f), .Qn(j_k_ff_1_qn), .preset(and_1_out), .reset(clr));  // open: en
  not not_1 (not_1_out, j_k_ff_1_qn);
  not not_2 (not_2_out, j_k_ff_3_qn);
  not not_3 (not_3_out, j_k_ff_5_qn);
  not not_4 (not_4_out, j_k_ff_6_qn);
  J_K_Flip_Flop j_k_ff_2 (
    .J(1'b1), .clk(f), .K(1'b1), .Q(e), .Qn(j_k_ff_2_qn), .preset(and_1_out), .reset(clr));  // open: en
  J_K_Flip_Flop j_k_ff_3 (
    .J(1'b1), .clk(e), .K(1'b1), .Q(d), .Qn(j_k_ff_3_qn), .preset(and_1_out), .reset(clr));  // open: en
  J_K_Flip_Flop j_k_ff_4 (
    .J(1'b1), .clk(d), .K(1'b1), .Q(c), .Qn(j_k_ff_4_qn), .preset(and_1_out), .reset(clr));  // open: en
  J_K_Flip_Flop j_k_ff_5 (
    .J(1'b1), .clk(c), .K(1'b1), .Q(b), .Qn(j_k_ff_5_qn), .preset(and_1_out), .reset(clr));  // open: en
  J_K_Flip_Flop j_k_ff_6 (
    .J(1'b1), .clk(b), .K(1'b1), .Q(a), .Qn(j_k_ff_6_qn), .preset(and_1_out), .reset(clr));  // open: en

  // Notes on the sheet:
  //   Matricula: 451580
  //   Isabel Bicalho Amaro
endmodule

module Questao5 (
  input  pulso,
  input  clear,
  output out_3,
  output out_4,
  output out_5,
  output out_6
);

  wire and_1_out, not_1_out, not_2_out, or_1_out, t_ff_2_qn, t_ff_3_qn, t_ff_4_qn;

  or or_1 (or_1_out, clear, and_1_out);
  and and_1 (and_1_out, out_3, not_1_out, out_5, not_2_out);
  T_Flip_Flop t_ff_1 (.clk(t_ff_2_qn), .T(t_ff_2_qn), .Q(out_3), .reset(or_1_out));  // open: Qn, preset, en
  not not_1 (not_1_out, out_4);
  not not_2 (not_2_out, out_6);
  T_Flip_Flop t_ff_2 (.clk(t_ff_3_qn), .T(t_ff_3_qn), .Q(out_4), .Qn(t_ff_2_qn), .reset(or_1_out));  // open: preset, en
  T_Flip_Flop t_ff_3 (.clk(t_ff_4_qn), .T(t_ff_4_qn), .Q(out_5), .Qn(t_ff_3_qn), .reset(or_1_out));  // open: preset, en
  T_Flip_Flop t_ff_4 (.clk(pulso), .T(pulso), .Q(out_6), .Qn(t_ff_4_qn));  // open: preset, reset, en

  // Notes on the sheet:
  //   Isabel Bicalho Amaro
  //   Matricula: 451580
endmodule
