// Logisim project Exercicio01.circ as structural Verilog: 1 circuit, main circuit main
module main (
  input  DATA,
  input  CLEAR,
  output out_3,
  output out_4,
  output out_5,
  output out_6,
  output out_7
);

  wire clock_1_out;

  Clock clock_1 (.out(clock_1_out));
  J_K_Flip_Flop j_k_ff_1 (.J(DATA), .clk(out_4), .K(DATA), .Qn(out_3), .reset(CLEAR));  // open: Q, preset, en
  J_K_Flip_Flop j_k_ff_2 (.J(DATA), .clk(out_5), .K(DATA), .Qn(out_4), .reset(CLEAR));  // open: Q, preset, en
  J_K_Flip_Flop j_k_ff_3 (.J(DATA), .clk(out_6), .K(DATA), .Qn(out_5), .reset(CLEAR));  // open: Q, preset, en
  J_K_Flip_Flop j_k_ff_4 (.J(DATA), .clk(out_7), .K(DATA), .Qn(out_6), .reset(CLEAR));  // open: Q, preset, en
  J_K_Flip_Flop j_k_ff_5 (.J(DATA), .clk(clock_1_out), .K(DATA), .Qn(out_7), .reset(CLEAR));  // open: Q, preset, en

  // Notes on the sheet:
  //   CLK
  //   Rodolfo herman - 451612
endmodule
