// Logisim project Exercicio03.circ as structural Verilog: 1 circuit, main circuit main
module main (
  input  DATA,
  input  in_2,
  output out_3,
  output out_4,
  output out_5,
  output out_6,
  output out_7,
  output out_8
);

  wire clock_1_out, j_k_ff_1_qn, j_k_ff_2_qn, j_k_ff_3_qn, j_k_ff_4_qn, j_k_ff_5_qn, nand_1_out, nand_2_out,
       not_1_out, not_2_out, not_3_out;

  Clock clock_1 (.out(clock_1_out));
  nand nand_1 (nand_1_out, in_2, nand_2_out);
  nand nand_2 (nand_2_out, not_1_out, out_7, not_2_out, out_5, not_3_out, out_3);
  J_K_Flip_Flop j_k_ff_1 (
    .J(DATA), .clk(clock_1_out), .K(DATA), .Q(out_8), .Qn(j_k_ff_1_qn), .reset(nand_1_out));  // open: preset, en
  not not_1 (not_1_out, out_8);
  not not_2 (not_2_out, out_6);
  not not_3 (not_3_out, out_4);
  J_K_Flip_Flop j_k_ff_2 (
    .J(DATA), .clk(j_k_ff_1_qn), .K(DATA), .Q(out_7), .Qn(j_k_ff_2_qn), .reset(nand_1_out));  // open: preset, en
  J_K_Flip_Flop j_k_ff_3 (
    .J(DATA), .clk(j_k_ff_2_qn), .K(DATA), .Q(out_6), .Qn(j_k_ff_3_qn), .reset(nand_1_out));  // open: preset, en
  J_K_Flip_Flop j_k_ff_4 (
    .J(DATA), .clk(j_k_ff_3_qn), .K(DATA), .Q(out_5), .Qn(j_k_ff_4_qn), .reset(nand_1_out));  // open: preset, en
  J_K_Flip_Flop j_k_ff_5 (
    .J(DATA), .clk(j_k_ff_4_qn), .K(DATA), .Q(out_4), .Qn(j_k_ff_5_qn), .reset(nand_1_out));  // open: preset, en
  J_K_Flip_Flop j_k_ff_6 (
    .J(DATA), .clk(j_k_ff_5_qn), .K(DATA), .Q(out_3), .reset(nand_1_out));  // open: Qn, preset, en

  // Notes on the sheet:
  //   CLK
  //   CLEAR
  //   Rodolfo Herman - 451612
endmodule
