// Logisim project Exercicio04.circ as structural Verilog: 1 circuit, main circuit main
module main (
  input  DATA,
  output out_2,
  output out_3,
  output out_4,
  output out_5,
  output out_6,
  output out_7
);

  wire and_1_out, clock_1_out, j_k_ff_1_qn, j_k_ff_2_qn, j_k_ff_3_qn, j_k_ff_4_qn, j_k_ff_5_qn, j_k_ff_6_qn,
       not_1_out, not_2_out, not_3_out, not_4_out, or_1_out;

  Clock clock_1 (.out(clock_1_out));
  not not_1 (not_1_out, DATA);
  or or_1 (or_1_out, not_1_out, and_1_out);
  and and_1 (and_1_out, not_2_out, j_k_ff_2_qn, not_3_out, j_k_ff_4_qn, not_4_out, j_k_ff_6_qn);
  J_K_Flip_Flop j_k_ff_1 (
    .J(DATA), .clk(clock_1_out), .K(DATA), .Q(out_7), .Qn(j_k_ff_1_qn), .preset(or_1_out));  // open: en, reset
  not not_2 (not_2_out, j_k_ff_1_qn);
  not not_3 (not_3_out, j_k_ff_3_qn);
  not not_4 (not_4_out, j_k_ff_5_qn);
  J_K_Flip_Flop j_k_ff_2 (
    .J(DATA), .clk(out_7), .K(DATA), .Q(out_6), .Qn(j_k_ff_2_qn), .preset(or_1_out));  // open: en, reset
  J_K_Flip_Flop j_k_ff_3 (
    .J(DATA), .clk(out_6), .K(DATA), .Q(out_5), .Qn(j_k_ff_3_qn), .preset(or_1_out));  // open: en, reset
  J_K_Flip_Flop j_k_ff_4 (
    .J(DATA), .clk(out_5), .K(DATA), .Q(out_4), .Qn(j_k_ff_4_qn), .preset(or_1_out));  // open: en, reset
  J_K_Flip_Flop j_k_ff_5 (
    .J(DATA), .clk(out_4), .K(DATA), .Q(out_3), .Qn(j_k_ff_5_qn), .preset(or_1_out));  // open: en, reset
  J_K_Flip_Flop j_k_ff_6 (
    .J(DATA), .clk(out_3), .K(DATA), .Q(out_2), .Qn(j_k_ff_6_qn), .preset(or_1_out));  // open: en, reset

  // Notes on the sheet:
  //   CLK
  //   Rodolfo Herman - 451612
endmodule
