// Logisim project Exercicio01.circ as structural Verilog: 1 circuit, main circuit main
module main (
  input  pulse,
  input  _1,
  input  clear,
  output a,
  output b,
  output c,
  output d,
  output e
);

  J_K_Flip_Flop j_k_ff_1 (.J(_1), .clk(b), .K(_1), .Qn(a), .reset(clear));  // open: Q, preset, en
  J_K_Flip_Flop j_k_ff_2 (.J(_1), .clk(c), .K(_1), .Qn(b), .reset(clear));  // open: Q, preset, en
  J_K_Flip_Flop j_k_ff_3 (.J(_1), .clk(d), .K(_1), .Qn(c), .reset(clear));  // open: Q, preset, en
  J_K_Flip_Flop j_k_ff_4 (.J(_1), .clk(e), .K(_1), .Qn(d), .reset(clear));  // open: Q, preset, en
  J_K_Flip_Flop j_k_ff_5 (.J(_1), .clk(pulse), .K(_1), .Qn(e), .reset(clear));  // open: Q, preset, en

  // Notes on the sheet:
  //   Matricula: 451620
  //   Exercicio01
  //   Nome: Tiago Matta Machado Zaidan
endmodule
