// Logisim project Exercicio02.circ as structural Verilog: 1 circuit, main circuit main
module main (
  input  pulse,
  input  _1,
  input  clear,
  output a,
  output b,
  output c,
  output d,
  output e
);

  wire j_k_ff_2_q, j_k_ff_3_q, j_k_ff_4_q, j_k_ff_5_q;

  J_K_Flip_Flop j_k_ff_1 (.J(_1), .clk(j_k_ff_2_q), .K(_1), .Qn(a), .reset(clear));  // open: Q, preset, en
  J_K_Flip_Flop j_k_ff_2 (.J(_1), .clk(j_k_ff_3_q), .K(_1), .Q(j_k_ff_2_q), .Qn(b), .reset(clear));  // open: preset, en
  J_K_Flip_Flop j_k_ff_3 (.J(_1), .clk(j_k_ff_4_q), .K(_1), .Q(j_k_ff_3_q), .Qn(c), .reset(clear));  // open: preset, en
  J_K_Flip_Flop j_k_ff_4 (.J(_1), .clk(j_k_ff_5_q), .K(_1), .Q(j_k_ff_4_q), .Qn(d), .reset(clear));  // open: preset, en
  J_K_Flip_Flop j_k_ff_5 (.J(_1), .clk(pulse), .K(_1), .Q(j_k_ff_5_q), .Qn(e), .reset(clear));  // open: preset, en

  // Notes on the sheet:
  //   Matricula: 451620
  //   Exercicio02
  //   Nome: Tiago Matta Machado Zaidan
endmodule
