// Logisim project Exercicio03.circ as structural Verilog: 1 circuit, main circuit main
module main (
  input  _1,
  input  pulse,
  input  clear,
  output a,
  output b,
  output c,
  output d,
  output e,
  output f
);

  wire j_k_ff_1_qn, j_k_ff_2_qn, j_k_ff_3_qn, j_k_ff_4_qn, j_k_ff_5_qn, nand_1_out, nand_2_out, not_1_out,
       not_2_out, not_3_out;

  nand nand_1 (nand_1_out, clear, nand_2_out);
  not not_1 (not_1_out, f);
  not not_2 (not_2_out, d);
  nand nand_2 (nand_2_out, not_1_out, e, not_2_out, c, not_3_out, a);
  not not_3 (not_3_out, b);
  J_K_Flip_Flop j_k_ff_1 (
    .J(_1), .clk(pulse), .K(_1), .Q(f), .Qn(j_k_ff_1_qn), .reset(nand_1_out));  // open: preset, en
  J_K_Flip_Flop j_k_ff_2 (
    .J(_1), .clk(j_k_ff_1_qn), .K(_1), .Q(e), .Qn(j_k_ff_2_qn), .reset(nand_1_out));  // open: preset, en
  J_K_Flip_Flop j_k_ff_3 (
    .J(_1), .clk(j_k_ff_2_qn), .K(_1), .Q(d), .Qn(j_k_ff_3_qn), .reset(nand_1_out));  // open: preset, en
  J_K_Flip_Flop j_k_ff_4 (
    .J(_1), .clk(j_k_ff_3_qn), .K(_1), .Q(c), .Qn(j_k_ff_4_qn), .reset(nand_1_out));  // open: preset, en
  J_K_Flip_Flop j_k_ff_5 (
    .J(_1), .clk(j_k_ff_4_qn), .K(_1), .Q(b), .Qn(j_k_ff_5_qn), .reset(nand_1_out));  // open: preset, en
  J_K_Flip_Flop j_k_ff_6 (.J(_1), .clk(j_k_ff_5_qn), .K(_1), .Q(a), .reset(nand_1_out));  // open: Qn, preset, en

  // Notes on the sheet:
  //   Matricula: 451620
  //   Exercicio03
  //   Nome: Tiago Matta Machado Zaidan
  //   Contador Decadico Crescente
endmodule
