// Logisim project EstudoDirigido09.circ as structural Verilog: 5 circuits, main circuit Exercicio01
module Exercicio01 (
  input  Clear,
  output out_2,
  output out_3,
  output out_4,
  output out_5,
  output out_6
);

  wire Clock_out;

  Clock Clock (.out(Clock_out));
  J_K_Flip_Flop j_k_ff_1 (.J(1'b1), .clk(out_3), .K(1'b1), .Qn(out_2), .reset(Clear));  // open: Q, preset, en
  J_K_Flip_Flop j_k_ff_2 (.J(1'b1), .clk(out_4), .K(1'b1), .Qn(out_3), .reset(Clear));  // open: Q, preset, en
  J_K_Flip_Flop j_k_ff_3 (.J(1'b1), .clk(out_5), .K(1'b1), .Qn(out_4), .reset(Clear));  // open: Q, preset, en
  J_K_Flip_Flop j_k_ff_4 (.J(1'b1), .clk(out_6), .K(1'b1), .Qn(out_5), .reset(Clear));  // open: Q, preset, en
  J_K_Flip_Flop j_k_ff_5 (.J(1'b1), .clk(Clock_out), .K(1'b1), .Qn(out_6), .reset(Clear));  // open: Q, preset, en
endmodule

module Exercicio02 (
  input  Clear,
  input  Initial,
  output out_3,
  output out_4,
  output out_5,
  output out_6,
  output out_7
);

  wire Clock_out, j_k_ff_2_q, j_k_ff_3_q, j_k_ff_4_q, j_k_ff_5_q;

  Clock Clock (.out(Clock_out));
  J_K_Flip_Flop j_k_ff_1 (.J(1'b1), .clk(j_k_ff_2_q), .K(1'b1), .Qn(out_3), .reset(Clear));  // open: Q, preset, en
  J_K_Flip_Flop j_k_ff_2 (
    .J(1'b1), .clk(j_k_ff_3_q), .K(1'b1), .Q(j_k_ff_2_q), .Qn(out_4), .reset(Clear));  // open: preset, en
  J_K_Flip_Flop j_k_ff_3 (
    .J(1'b1), .clk(j_k_ff_4_q), .K(1'b1), .Q(j_k_ff_3_q), .Qn(out_5), .reset(Clear));  // open: preset, en
  J_K_Flip_Flop j_k_ff_4 (
    .J(1'b1), .clk(j_k_ff_5_q), .K(1'b1), .Q(j_k_ff_4_q), .Qn(out_6), .reset(Clear));  // open: preset, en
  J_K_Flip_Flop j_k_ff_5 (
    .J(1'b1), .clk(Clock_out), .K(1'b1), .Q(j_k_ff_5_q), .Qn(out_7), .preset(Initial), .reset(Clear));  // open: en

  // Notes on the sheet:
  //   Wadson Ferreira - 460631
endmodule

module Exercicio03 (
  input  in_1,
  output out_2,
  output out_3,
  output out_4,
  output out_5,
  output out_6,
  output out_7
);

  wire and_1_out, clock_1_out, j_k_ff_1_qn, j_k_ff_2_qn, j_k_ff_3_qn, j_k_ff_4_qn, j_k_ff_5_qn, j_k_ff_6_qn,
       or_1_out;

  Clock clock_1 (.out(clock_1_out));
  J_K_Flip_Flop j_k_ff_1 (
    .J(1'b1), .clk(clock_1_out), .K(1'b1), .Q(out_7), .Qn(j_k_ff_1_qn), .reset(or_1_out));  // open: preset, en
  or or_1 (or_1_out, in_1, and_1_out);
  and and_1 (and_1_out, j_k_ff_1_qn, out_6, j_k_ff_3_qn, out_4, j_k_ff_5_qn, j_k_ff_6_qn);
  J_K_Flip_Flop j_k_ff_2 (
    .J(1'b1), .clk(j_k_ff_1_qn), .K(1'b1), .Q(out_6), .Qn(j_k_ff_2_qn), .reset(or_1_out));  // open: preset, en
  J_K_Flip_Flop j_k_ff_3 (
    .J(1'b1), .clk(j_k_ff_2_qn), .K(1'b1), .Q(out_5), .Qn(j_k_ff_3_qn), .reset(or_1_out));  // open: preset, en
  J_K_Flip_Flop j_k_ff_4 (
    .J(1'b1), .clk(j_k_ff_3_qn), .K(1'b1), .Q(out_4), .Qn(j_k_ff_4_qn), .reset(or_1_out));  // open: preset, en
  J_K_Flip_Flop j_k_ff_5 (
    .J(1'b1), .clk(j_k_ff_4_qn), .K(1'b1), .Q(out_3), .Qn(j_k_ff_5_qn), .reset(or_1_out));  // open: preset, en
  J_K_Flip_Flop j_k_ff_6 (
    .J(1'b1), .clk(j_k_ff_5_qn), .K(1'b1), .Q(out_2), .Qn(j_k_ff_6_qn), .reset(or_1_out));  // open: preset, en

  // Notes on the sheet:
  //   Wadson Ferreira - 460631
endmodule

module Exercicio04 (
  input  in_1,
  output out_2,
  output out_3,
  output out_4,
  output out_5,
  output out_6,
  output out_7
);

  wire and_1_out, clock_1_out, j_k_ff_2_qn, j_k_ff_4_qn;

  Clock clock_1 (.out(clock_1_out));
  J_K_Flip_Flop j_k_ff_1 (
    .J(1'b1), .clk(clock_1_out), .K(1'b1), .Q(out_7), .preset(and_1_out), .reset(in_1));  // open: Qn, en
  and and_1 (and_1_out, out_7, j_k_ff_2_qn, out_5, j_k_ff_4_qn, out_3, out_2);
  J_K_Flip_Flop j_k_ff_2 (
    .J(1'b1), .clk(out_7), .K(1'b1), .Q(out_6), .Qn(j_k_ff_2_qn), .preset(and_1_out), .reset(in_1));  // open: en
  J_K_Flip_Flop j_k_ff_3 (
    .J(1'b1), .clk(out_6), .K(1'b1), .Q(out_5), .preset(and_1_out), .reset(in_1));  // open: Qn, en
  J_K_Flip_Flop j_k_ff_4 (
    .J(1'b1), .clk(out_5), .K(1'b1), .Q(out_4), .Qn(j_k_ff_4_qn), .preset(and_1_out), .reset(in_1));  // open: en
  J_K_Flip_Flop j_k_ff_5 (
    .J(1'b1), .clk(out_4), .K(1'b1), .Q(out_3), .preset(and_1_out), .reset(in_1));  // open: Qn, en
  J_K_Flip_Flop j_k_ff_6 (
    .J(1'b1), .clk(out_3), .K(1'b1), .Q(out_2), .preset(and_1_out), .reset(in_1));  // open: Qn, en

  // Notes on the sheet:
  //   Wadson Ferreira - 460631
endmodule

module Exercicio05 (
  input  Clear,
  output out_2,
  output out_3,
  output out_4,
  output out_5
);

  wire and_1_out, Clock_out, or_1_out, t_ff_1_qn, t_ff_2_qn, t_ff_3_qn;

  Clock Clock (.out(Clock_out));
  and and_1 (and_1_out, t_ff_1_qn, out_4, t_ff_3_qn, out_2);
  T_Flip_Flop t_ff_1 (.clk(Clock_out), .T(Clock_out), .Q(out_5), .Qn(t_ff_1_qn), .reset(or_1_out));  // open: preset, en
  or or_1 (or_1_out, Clear, and_1_out);
  T_Flip_Flop t_ff_2 (.clk(t_ff_1_qn), .T(t_ff_1_qn), .Q(out_4), .Qn(t_ff_2_qn), .reset(or_1_out));  // open: preset, en
  T_Flip_Flop t_ff_3 (.clk(t_ff_2_qn), .T(t_ff_2_qn), .Q(out_3), .Qn(t_ff_3_qn), .reset(or_1_out));  // open: preset, en
  T_Flip_Flop t_ff_4 (.clk(t_ff_3_qn), .T(t_ff_3_qn), .Q(out_2), .reset(or_1_out));  // open: Qn, preset, en

  // Notes on the sheet:
  //   Wadson Ferreira - 460631
endmodule
