// Logisim project contador decadico crescente.circ as structural Verilog: 1 circuit, main circuit main
module main (
  input  in_1,
  input  in_2,
  output out_3,
  output out_4,
  output out_5,
  output out_6,
  output out_7,
  output out_8
);

  wire clock_1_out, j_k_ff_1_qn, j_k_ff_2_qn, j_k_ff_3_qn, j_k_ff_4_qn, j_k_ff_5_qn, nand_1_out, nand_2_out;

  Clock clock_1 (.out(clock_1_out));
  J_K_Flip_Flop j_k_ff_1 (
    .J(in_1), .clk(clock_1_out), .K(in_1), .Q(out_8), .Qn(j_k_ff_1_qn), .reset(nand_1_out));  // open: preset, en
  nand nand_1 (nand_1_out, in_2, nand_2_out);
  nand nand_2 (nand_2_out, ~out_8, out_7, ~out_6, out_5, ~out_4, ~out_3);  // NAND_Gate
  J_K_Flip_Flop j_k_ff_2 (
    .J(in_1), .clk(j_k_ff_1_qn), .K(in_1), .Q(out_7), .Qn(j_k_ff_2_qn), .reset(nand_1_out));  // open: preset, en
  J_K_Flip_Flop j_k_ff_3 (
    .J(in_1), .clk(j_k_ff_2_qn), .K(in_1), .Q(out_6), .Qn(j_k_ff_3_qn), .reset(nand_1_out));  // open: preset, en
  J_K_Flip_Flop j_k_ff_4 (
    .J(in_1), .clk(j_k_ff_3_qn), .K(in_1), .Q(out_5), .Qn(j_k_ff_4_qn), .reset(nand_1_out));  // open: preset, en
  J_K_Flip_Flop j_k_ff_5 (
    .J(in_1), .clk(j_k_ff_4_qn), .K(in_1), .Q(out_4), .Qn(j_k_ff_5_qn), .reset(nand_1_out));  // open: preset, en
  J_K_Flip_Flop j_k_ff_6 (
    .J(in_1), .clk(j_k_ff_5_qn), .K(in_1), .Q(out_3), .reset(nand_1_out));  // open: Qn, preset, en
endmodule
