// Logisim project contador em anel torcido.circ as structural Verilog: 1 circuit, main circuit main
module main (
  input  in_1,
  input  in_2,
  input  in_3,
  output out_4,
  output out_5,
  output out_6,
  output out_7,
  output out_8,
  output out_9,
  output out_10,
  output out_11,
  output out_12
);

  wire clock_1_out, clock_2_out, d_ff_3_qn, j_k_ff_1_qn, j_k_ff_2_qn, j_k_ff_3_qn, j_k_ff_4_qn, j_k_ff_5_qn,
       j_k_ff_6_qn, or_1_out;

  Clock clock_1 (.out(clock_1_out));
  Clock clock_2 (.out(clock_2_out));
  J_K_Flip_Flop j_k_ff_1 (
    .J(j_k_ff_6_qn), .clk(clock_1_out), .K(out_9), .Q(out_4), .Qn(j_k_ff_1_qn), .reset(in_1));  // open: preset, en
  D_Flip_Flop d_ff_1 (.clk(clock_2_out), .D(or_1_out), .Q(out_10), .reset(in_3));  // open: Qn, preset, en
  or or_1 (or_1_out, in_2, d_ff_3_qn);
  J_K_Flip_Flop j_k_ff_2 (
    .J(out_4), .clk(clock_1_out), .K(j_k_ff_1_qn), .Q(out_5), .Qn(j_k_ff_2_qn), .reset(in_1));  // open: preset, en
  J_K_Flip_Flop j_k_ff_3 (
    .J(out_5), .clk(clock_1_out), .K(j_k_ff_2_qn), .Q(out_6), .Qn(j_k_ff_3_qn), .reset(in_1));  // open: preset, en
  D_Flip_Flop d_ff_2 (.clk(clock_2_out), .D(out_10), .Q(out_11), .reset(in_3));  // open: Qn, preset, en
  J_K_Flip_Flop j_k_ff_4 (
    .J(out_6), .clk(clock_1_out), .K(j_k_ff_3_qn), .Q(out_7), .Qn(j_k_ff_4_qn), .reset(in_1));  // open: preset, en
  D_Flip_Flop d_ff_3 (.clk(clock_2_out), .D(out_11), .Q(out_12), .Qn(d_ff_3_qn), .reset(in_3));  // open: preset, en
  J_K_Flip_Flop j_k_ff_5 (
    .J(out_7), .clk(clock_1_out), .K(j_k_ff_4_qn), .Q(out_8), .Qn(j_k_ff_5_qn), .reset(in_1));  // open: preset, en
  J_K_Flip_Flop j_k_ff_6 (
    .J(out_8), .clk(clock_1_out), .K(j_k_ff_5_qn), .Q(out_9), .Qn(j_k_ff_6_qn), .reset(in_1));  // open: preset, en
endmodule
