// Logisim project contador em anel.circ as structural Verilog: 1 circuit, main circuit main
module main (
  input  in_1,
  input  in_2,
  input  in_3,
  input  in_4,
  output out_5,
  output out_6,
  output out_7,
  output out_8,
  output out_9,
  output out_10,
  output out_11,
  output out_12,
  output out_13
);

  wire clock_1_out, clock_2_out, not_1_out, not_2_out, not_3_out, not_4_out, not_5_out, not_6_out, or_1_out,
       or_2_out;

  Clock clock_1 (.out(clock_1_out));
  Clock clock_2 (.out(clock_2_out));
  or or_1 (or_1_out, out_10, in_1);
  not not_1 (not_1_out, or_1_out);
  D_Flip_Flop d_ff_1 (.clk(clock_2_out), .D(or_2_out), .Q(out_11), .reset(in_4));  // open: Qn, preset, en
  or or_2 (or_2_out, out_13, in_3);
  J_K_Flip_Flop j_k_ff_1 (
    .J(or_1_out), .clk(clock_1_out), .K(not_1_out), .Q(out_5), .reset(in_2));  // open: Qn, preset, en
  not not_2 (not_2_out, out_5);
  J_K_Flip_Flop j_k_ff_2 (
    .J(out_5), .clk(clock_1_out), .K(not_2_out), .Q(out_6), .reset(in_2));  // open: Qn, preset, en
  D_Flip_Flop d_ff_2 (.clk(clock_2_out), .D(out_11), .Q(out_12), .reset(in_4));  // open: Qn, preset, en
  J_K_Flip_Flop j_k_ff_3 (
    .J(out_6), .clk(clock_1_out), .K(not_3_out), .Q(out_7), .reset(in_2));  // open: Qn, preset, en
  not not_3 (not_3_out, out_6);
  D_Flip_Flop d_ff_3 (.clk(clock_2_out), .D(out_12), .Q(out_13), .reset(in_4));  // open: Qn, preset, en
  J_K_Flip_Flop j_k_ff_4 (
    .J(out_7), .clk(clock_1_out), .K(not_4_out), .Q(out_8), .reset(in_2));  // open: Qn, preset, en
  not not_4 (not_4_out, out_7);
  not not_5 (not_5_out, out_8);
  J_K_Flip_Flop j_k_ff_5 (
    .J(out_8), .clk(clock_1_out), .K(not_5_out), .Q(out_9), .reset(in_2));  // open: Qn, preset, en
  not not_6 (not_6_out, out_9);
  J_K_Flip_Flop j_k_ff_6 (
    .J(out_9), .clk(clock_1_out), .K(not_6_out), .Q(out_10), .reset(in_2));  // open: Qn, preset, en
endmodule
