// Logisim project contador modulo 10.circ as structural Verilog: 1 circuit, main circuit main
module main (
  input  in_1,
  output out_2,
  output out_3,
  output out_4,
  output out_5
);

  wire and_1_out, clock_1_out, or_1_out, t_ff_2_qn, t_ff_3_qn, t_ff_4_qn;

  Clock clock_1 (.out(clock_1_out));
  or or_1 (or_1_out, in_1, and_1_out);
  T_Flip_Flop t_ff_1 (.clk(t_ff_2_qn), .T(t_ff_2_qn), .Q(out_2), .reset(or_1_out));  // open: Qn, preset, en
  and and_1 (and_1_out, out_2, ~out_3, out_4, ~out_5);  // AND_Gate
  T_Flip_Flop t_ff_2 (.clk(t_ff_3_qn), .T(t_ff_3_qn), .Q(out_3), .Qn(t_ff_2_qn), .reset(or_1_out));  // open: preset, en
  T_Flip_Flop t_ff_3 (.clk(t_ff_4_qn), .T(t_ff_4_qn), .Q(out_4), .Qn(t_ff_3_qn), .reset(or_1_out));  // open: preset, en
  T_Flip_Flop t_ff_4 (
    .clk(clock_1_out), .T(clock_1_out), .Q(out_5), .Qn(t_ff_4_qn), .reset(or_1_out));  // open: preset, en
endmodule
