// Logisim project Exercicio03.circ as structural Verilog: 1 circuit, main circuit main
module main (
  input  in_1,
  input  Clear,
  output out_3,
  output out_4,
  output out_5,
  output out_6,
  output out_7,
  output out_8
);

  wire Clk_out, j_k_ff_1_qn, j_k_ff_2_qn, j_k_ff_3_qn, j_k_ff_4_qn, j_k_ff_5_qn, j_k_ff_6_qn, nand_1_out,
       nand_2_out, not_1_out, not_2_out;

  Clock Clk (.out(Clk_out));
  nand nand_1 (nand_1_out, j_k_ff_1_qn, j_k_ff_2_qn, not_1_out, j_k_ff_4_qn, not_2_out, j_k_ff_6_qn);
  J_K_Flip_Flop j_k_ff_1 (
    .J(in_1), .clk(j_k_ff_2_qn), .K(in_1), .Q(out_3), .Qn(j_k_ff_1_qn), .reset(nand_2_out));  // open: preset, en
  nand nand_2 (nand_2_out, Clear, nand_1_out);
  not not_1 (not_1_out, j_k_ff_3_qn);
  not not_2 (not_2_out, j_k_ff_5_qn);
  J_K_Flip_Flop j_k_ff_2 (
    .J(in_1), .clk(j_k_ff_3_qn), .K(in_1), .Q(out_4), .Qn(j_k_ff_2_qn), .reset(nand_2_out));  // open: preset, en
  J_K_Flip_Flop j_k_ff_3 (
    .J(in_1), .clk(j_k_ff_4_qn), .K(in_1), .Q(out_5), .Qn(j_k_ff_3_qn), .reset(nand_2_out));  // open: preset, en
  J_K_Flip_Flop j_k_ff_4 (
    .J(in_1), .clk(j_k_ff_5_qn), .K(in_1), .Q(out_6), .Qn(j_k_ff_4_qn), .reset(nand_2_out));  // open: preset, en
  J_K_Flip_Flop j_k_ff_5 (
    .J(in_1), .clk(j_k_ff_6_qn), .K(in_1), .Q(out_7), .Qn(j_k_ff_5_qn), .reset(nand_2_out));  // open: preset, en
  J_K_Flip_Flop j_k_ff_6 (
    .J(in_1), .clk(Clk_out), .K(in_1), .Q(out_8), .Qn(j_k_ff_6_qn), .reset(nand_2_out));  // open: preset, en

  // Notes on the sheet:
  //   462017
  //   Breno Macena Pereira de Souza
endmodule
