// Logisim project Exercicio04.circ as structural Verilog: 1 circuit, main circuit main
module main (
  input  in_1,
  input  Clear,
  output out_3,
  output out_4,
  output out_5,
  output out_6,
  output out_7,
  output out_8
);

  wire Clk_out, nand_1_out, nand_2_out, not_1_out, not_2_out;

  Clock Clk (.out(Clk_out));
  nand nand_1 (nand_1_out, out_3, out_4, not_1_out, out_6, not_2_out, out_8);
  J_K_Flip_Flop j_k_ff_1 (.J(in_1), .clk(out_4), .K(in_1), .Q(out_3), .reset(nand_2_out));  // open: Qn, preset, en
  nand nand_2 (nand_2_out, Clear, nand_1_out);
  not not_1 (not_1_out, out_5);
  not not_2 (not_2_out, out_7);
  J_K_Flip_Flop j_k_ff_2 (.J(in_1), .clk(out_5), .K(in_1), .Q(out_4), .reset(nand_2_out));  // open: Qn, preset, en
  J_K_Flip_Flop j_k_ff_3 (.J(in_1), .clk(out_6), .K(in_1), .Q(out_5), .reset(nand_2_out));  // open: Qn, preset, en
  J_K_Flip_Flop j_k_ff_4 (.J(in_1), .clk(out_7), .K(in_1), .Q(out_6), .reset(nand_2_out));  // open: Qn, preset, en
  J_K_Flip_Flop j_k_ff_5 (.J(in_1), .clk(out_8), .K(in_1), .Q(out_7), .reset(nand_2_out));  // open: Qn, preset, en
  J_K_Flip_Flop j_k_ff_6 (.J(in_1), .clk(Clk_out), .K(in_1), .Q(out_8), .reset(nand_2_out));  // open: Qn, preset, en

  // Notes on the sheet:
  //   Breno Macena Pereira de Souza
  //   462017
endmodule
