// Logisim project Exercicio05.circ as structural Verilog: 1 circuit, main circuit main
module main (
  input  Clear,
  output out_2,
  output out_3,
  output out_4,
  output out_5
);

  wire and_1_out, Clk_out, not_1_out, not_2_out, or_1_out, t_ff_2_qn, t_ff_3_qn, t_ff_4_qn;

  Clock Clk (.out(Clk_out));
  or or_1 (or_1_out, Clear, and_1_out);
  and and_1 (and_1_out, out_2, not_1_out, out_4, not_2_out);
  T_Flip_Flop t_ff_1 (.clk(t_ff_2_qn), .T(t_ff_2_qn), .Q(out_2), .reset(or_1_out));  // open: Qn, preset, en
  not not_1 (not_1_out, out_3);
  not not_2 (not_2_out, out_5);
  T_Flip_Flop t_ff_2 (.clk(t_ff_3_qn), .T(t_ff_3_qn), .Q(out_3), .Qn(t_ff_2_qn), .reset(or_1_out));  // open: preset, en
  T_Flip_Flop t_ff_3 (.clk(t_ff_4_qn), .T(t_ff_4_qn), .Q(out_4), .Qn(t_ff_3_qn), .reset(or_1_out));  // open: preset, en
  T_Flip_Flop t_ff_4 (.clk(Clk_out), .T(Clk_out), .Q(out_5), .Qn(t_ff_4_qn), .reset(or_1_out));  // open: preset, en

  // Notes on the sheet:
  //   Breno Macena Pereira de Souza
  //   462017
endmodule
