// Logisim project Exercicio06.circ as structural Verilog: 1 circuit, main circuit main
module main (
  input  in_1,
  input  Clear,
  output out_3,
  output out_4,
  output out_5,
  output out_6,
  output out_7,
  output out_8
);

  wire CLK_out, or_1_out;

  Clock CLK (.out(CLK_out));
  J_K_Flip_Flop j_k_ff_1 (.J(in_1), .clk(out_4), .K(in_1), .Q(out_3), .reset(Clear));  // open: Qn, preset, en
  J_K_Flip_Flop j_k_ff_2 (.J(in_1), .clk(out_5), .K(in_1), .Q(out_4), .reset(Clear));  // open: Qn, preset, en
  J_K_Flip_Flop j_k_ff_3 (.J(in_1), .clk(out_6), .K(in_1), .Q(out_5), .reset(Clear));  // open: Qn, preset, en
  J_K_Flip_Flop j_k_ff_4 (.J(in_1), .clk(out_7), .K(in_1), .Q(out_6), .reset(Clear));  // open: Qn, preset, en
  J_K_Flip_Flop j_k_ff_5 (.J(in_1), .clk(out_8), .K(in_1), .Q(out_7), .reset(Clear));  // open: Qn, preset, en
  or or_1 (or_1_out, out_3, in_1);
  J_K_Flip_Flop j_k_ff_6 (.J(or_1_out), .clk(CLK_out), .K(or_1_out), .Q(out_8), .reset(Clear));  // open: Qn, preset, en

  // Notes on the sheet:
  //   462017
  //   Breno Macena Pereira de Souza
endmodule
