// Logisim project Exercicio07.circ as structural Verilog: 1 circuit, main circuit main
module main (
  input  in_1,
  input  in_2,
  output out_3,
  output out_4,
  output out_5,
  output out_6,
  output out_7,
  output out_8
);

  wire and_1_out, and_2_out, and_3_out, and_4_out, clock_1_out, j_k_ff_1_qn, or_1_out;

  Clock clock_1 (.out(clock_1_out));
  and and_1 (and_1_out, out_4, out_5, out_6, out_7, out_8);
  J_K_Flip_Flop j_k_ff_1 (
    .J(and_1_out), .clk(clock_1_out), .K(and_1_out), .Q(out_3), .Qn(j_k_ff_1_qn), .reset(in_2));  // open: preset, en
  and and_2 (and_2_out, out_5, out_6, out_7, out_8);
  or or_1 (or_1_out, j_k_ff_1_qn, in_1);
  J_K_Flip_Flop j_k_ff_2 (
    .J(and_2_out), .clk(clock_1_out), .K(and_2_out), .Q(out_4), .reset(in_2));  // open: Qn, preset, en
  and and_3 (and_3_out, out_6, out_7, out_8);
  J_K_Flip_Flop j_k_ff_3 (
    .J(and_3_out), .clk(clock_1_out), .K(and_3_out), .Q(out_5), .reset(in_2));  // open: Qn, preset, en
  and and_4 (and_4_out, out_7, out_8);
  J_K_Flip_Flop j_k_ff_4 (
    .J(and_4_out), .clk(clock_1_out), .K(and_4_out), .Q(out_6), .reset(in_2));  // open: Qn, preset, en
  J_K_Flip_Flop j_k_ff_5 (.J(out_8), .clk(clock_1_out), .K(out_8), .Q(out_7), .reset(in_2));  // open: Qn, preset, en
  J_K_Flip_Flop j_k_ff_6 (
    .J(or_1_out), .clk(clock_1_out), .K(or_1_out), .Q(out_8), .reset(in_2));  // open: Qn, preset, en

  // Notes on the sheet:
  //   462017
  //   Breno Macena Pereira de Souza
endmodule
