// Logisim project guia10.circ as structural Verilog: 8 circuits, main circuit main
module main (
);


  // Notes on the sheet:
  //   Lucas Siqueira Chagas - 380784
  //   Modulos na lista a esquerda
endmodule

// 1x4
module mem1x4 (
  input  CLK,
  input  [3:0] IN,
  input  R_W,
  input  ADDRESS,
  input  CLR,
  output [3:0] OUT
);

  wire and_1_out, not_1_out, not_2_out, not_3_out, not_4_out;
  wire [3:0] j_k_ff_4_q;

  and and_1 (and_1_out, CLK, R_W, ADDRESS);
  J_K_Flip_Flop j_k_ff_1 (
    .J(IN[3]), .clk(and_1_out), .K(not_1_out), .Q(j_k_ff_4_q[3]), .reset(CLR));  // open: Qn, preset, en
  not not_1 (not_1_out, IN[3]);
  not not_2 (not_2_out, IN[2]);
  J_K_Flip_Flop j_k_ff_2 (
    .J(IN[2]), .clk(and_1_out), .K(not_2_out), .Q(j_k_ff_4_q[2]), .reset(CLR));  // open: Qn, preset, en
  J_K_Flip_Flop j_k_ff_3 (
    .J(IN[1]), .clk(and_1_out), .K(not_3_out), .Q(j_k_ff_4_q[1]), .reset(CLR));  // open: Qn, preset, en
  not not_3 (not_3_out, IN[1]);
  not not_4 (not_4_out, IN[0]);
  J_K_Flip_Flop j_k_ff_4 (
    .J(IN[0]), .clk(and_1_out), .K(not_4_out), .Q(j_k_ff_4_q[0]), .reset(CLR));  // open: Qn, preset, en
  assign OUT = j_k_ff_4_q & {4{ADDRESS}};  // AND_Gate and_2, 4 bits wide
endmodule

// 2X4
module mem2x4 (
  input  CLK,
  input  R_W,
  input  ADRESS,
  input  [3:0] IN,
  input  CLR,
  output [3:0] OUT
);

  wire demultiplexer_1_out0, demultiplexer_1_out1;
  wire [3:0] mem1x4_2_out, MEM1x4_out;

  Demultiplexer #(.enable("false")) demultiplexer_1 (
    .out0(demultiplexer_1_out0), .out1(demultiplexer_1_out1), .in(1'b1), .sel(ADRESS));
  mem1x4 MEM1x4 (.CLK(CLK), .R_W(R_W), .ADDRESS(demultiplexer_1_out0), .CLR(CLR), .IN(IN), .OUT(MEM1x4_out));
  mem1x4 mem1x4_2 (.CLK(CLK), .R_W(R_W), .ADDRESS(demultiplexer_1_out1), .CLR(CLR), .IN(IN), .OUT(mem1x4_2_out));
  Multiplexer #(.width(4), .enable("false")) multiplexer_1 (
    .in0(MEM1x4_out), .in1(mem1x4_2_out), .out(OUT), .sel(ADRESS));
endmodule

// 1x8
module mem1x8 (
  input  CLK,
  input  R_W,
  input  ADDRESS,
  input  [7:0] IN,
  input  CLR,
  output [7:0] OUT
);

  mem1x4 mem1x4_1 (.CLK(CLK), .R_W(R_W), .ADDRESS(ADDRESS), .CLR(CLR), .IN(IN[3:0]), .OUT(OUT[3:0]));
  mem1x4 mem1x4_2 (.CLK(CLK), .R_W(R_W), .ADDRESS(ADDRESS), .CLR(CLR), .IN(IN[7:4]), .OUT(OUT[7:4]));
endmodule

// 4X8
module mem4x8 (
  input  CLK,
  input  [7:0] IN,
  input  R_W,
  input  [1:0] ADRESS,
  input  CLR,
  output [7:0] OUT
);

  wire demultiplexer_1_out0, demultiplexer_1_out1, demultiplexer_1_out2, demultiplexer_1_out3;
  wire [3:0] mem1x4_1_out, mem1x4_2_out, mem1x4_3_out, mem1x4_4_out, mem1x4_5_out, mem1x4_6_out,
       mem1x4_7_out, mem1x4_8_out;

  Demultiplexer #(.select(2), .enable("false")) demultiplexer_1 (
    .out0(demultiplexer_1_out0), .out1(demultiplexer_1_out1), .out2(demultiplexer_1_out2),
    .out3(demultiplexer_1_out3), .in(1'b1), .sel(ADRESS));
  mem1x4 mem1x4_1 (.CLK(CLK), .R_W(R_W), .ADDRESS(demultiplexer_1_out0), .CLR(CLR), .IN(IN[7:4]), .OUT(mem1x4_1_out));
  mem1x4 mem1x4_2 (.CLK(CLK), .R_W(R_W), .ADDRESS(demultiplexer_1_out1), .CLR(CLR), .IN(IN[7:4]), .OUT(mem1x4_2_out));
  mem1x4 mem1x4_3 (.CLK(CLK), .R_W(R_W), .ADDRESS(demultiplexer_1_out2), .CLR(CLR), .IN(IN[7:4]), .OUT(mem1x4_3_out));
  mem1x4 mem1x4_4 (.CLK(CLK), .R_W(R_W), .ADDRESS(demultiplexer_1_out3), .CLR(CLR), .IN(IN[7:4]), .OUT(mem1x4_4_out));
  Multiplexer #(.select(2), .width(4), .enable("false")) multiplexer_1 (
    .in0(mem1x4_1_out), .in1(mem1x4_2_out), .in2(mem1x4_3_out), .in3(mem1x4_4_out), .out(OUT[7:4]),
    .sel(ADRESS));
  mem1x4 mem1x4_5 (.CLK(CLK), .R_W(R_W), .ADDRESS(demultiplexer_1_out0), .CLR(CLR), .IN(IN[3:0]), .OUT(mem1x4_5_out));
  mem1x4 mem1x4_6 (.CLK(CLK), .R_W(R_W), .ADDRESS(demultiplexer_1_out1), .CLR(CLR), .IN(IN[3:0]), .OUT(mem1x4_6_out));
  mem1x4 mem1x4_7 (.CLK(CLK), .R_W(R_W), .ADDRESS(demultiplexer_1_out2), .CLR(CLR), .IN(IN[3:0]), .OUT(mem1x4_7_out));
  mem1x4 mem1x4_8 (.CLK(CLK), .R_W(R_W), .ADDRESS(demultiplexer_1_out3), .CLR(CLR), .IN(IN[3:0]), .OUT(mem1x4_8_out));
  Multiplexer #(.select(2), .width(4), .enable("false")) multiplexer_2 (
    .in0(mem1x4_5_out), .in1(mem1x4_6_out), .in2(mem1x4_7_out), .in3(mem1x4_8_out), .out(OUT[3:0]),
    .sel(ADRESS));
endmodule

module MEM8X8 (
  input  CLK,
  input  R_W,
  input  [7:0] IN,
  input  [2:0] ADRESS,
  input  CLR,
  output [7:0] OUT
);

  wire [1:0] demultiplexer_1_out0, demultiplexer_1_out1;

  Demultiplexer #(.width(2), .enable("false")) demultiplexer_1 (
    .out0(demultiplexer_1_out0), .out1(demultiplexer_1_out1), .in(ADRESS[1:0]), .sel(ADRESS[2]));
  mem4x8 mem4x8_1 (.CLK(CLK), .R_W(R_W), .ADRESS(demultiplexer_1_out0), .CLR(CLR), .IN(IN), .OUT(OUT));
  mem4x8 mem4x8_2 (.CLK(CLK), .R_W(R_W), .ADRESS(demultiplexer_1_out1), .CLR(CLR), .IN(IN), .OUT(OUT));
endmodule

module mem1x16 (
  input  R_W,
  input  CLK,
  input  [15:0] IN,
  output [15:0] OUT
);

  mem1x8 mem1x8_1 (.CLK(CLK), .R_W(R_W), .ADDRESS(1'b1), .IN(IN[7:0]), .OUT(OUT[7:0]));  // open: CLR
  mem1x8 mem1x8_2 (.CLK(CLK), .R_W(R_W), .ADDRESS(1'b1), .IN(IN[15:8]), .OUT(OUT[15:8]));  // open: CLR
endmodule

module mem4x8b (
  input  CLK,
  input  R_W,
  input  [7:0] IN,
  input  [1:0] in_4,
  output [7:0] OUT
);

  wire demultiplexer_1_out0, demultiplexer_1_out1, demultiplexer_1_out2, demultiplexer_1_out3;
  wire [7:0] mem1x8_1_out, mem1x8_2_out, mem1x8_3_out, mem1x8_4_out;

  Demultiplexer #(.select(2), .enable("false")) demultiplexer_1 (
    .out0(demultiplexer_1_out0), .out1(demultiplexer_1_out1), .out2(demultiplexer_1_out2),
    .out3(demultiplexer_1_out3), .in(1'b1), .sel(in_4));
  mem1x8 mem1x8_1 (.R_W(R_W), .ADDRESS(demultiplexer_1_out0), .IN(IN), .OUT(mem1x8_1_out));  // open: CLK, CLR
  mem1x8 mem1x8_2 (.CLK(CLK), .R_W(R_W), .ADDRESS(demultiplexer_1_out1), .IN(IN), .OUT(mem1x8_2_out));  // open: CLR
  mem1x8 mem1x8_3 (.CLK(CLK), .R_W(R_W), .ADDRESS(demultiplexer_1_out2), .IN(IN), .OUT(mem1x8_3_out));  // open: CLR
  mem1x8 mem1x8_4 (.CLK(CLK), .R_W(R_W), .ADDRESS(demultiplexer_1_out3), .IN(IN), .OUT(mem1x8_4_out));  // open: CLR
  Multiplexer #(.select(2), .width(8), .enable("false")) multiplexer_1 (
    .in0(mem1x8_1_out), .in1(mem1x8_2_out), .in2(mem1x8_3_out), .in3(mem1x8_4_out), .out(OUT), .sel(in_4));
endmodule
