// Logisim project CIRCUITOS_Guia10.circ as structural Verilog: 7 circuits, main circuit main
module main (
  input  CLK,
  input  CLK_2,
  input  CLK_3,
  input  [3:0] IN,
  input  [7:0] IN_2,
  input  [7:0] IN_3,
  input  R_W,
  input  R_W_2,
  input  R_W_3,
  input  Addr,
  input  [1:0] Addr_2,
  input  [1:0] Addr_3,
  input  CLEAR,
  input  CLEAR_2,
  input  CLEAR_3,
  input  CLK_4,
  input  CLK_5,
  input  [3:0] IN_4,
  input  [7:0] IN_5,
  input  R_W_4,
  input  R_W_5,
  input  Addr_4,
  input  [2:0] Addr_5,
  input  CLEAR_4,
  input  CLEAR_5,
  input  CLK_6,
  input  CLK_7,
  input  [15:0] IN_6,
  input  [7:0] IN_7,
  input  R_W_6,
  input  R_W_7,
  input  Addr_6,
  input  Addr_7,
  input  CLEAR_6,
  input  CLEAR_7,
  output [3:0] OUT,
  output [7:0] OUT_2,
  output [7:0] OUT_3,
  output [3:0] OUT_4,
  output [7:0] OUT_5,
  output [7:0] OUT_6,
  output [15:0] OUT_7
);

  RAM_1x4 RAM (.CLK(CLK), .R_W(R_W), .Addr(Addr), .IN(IN), .OUT(OUT), .CLR(CLEAR));
  RAM_2x4 RAM_2 (.CLK(CLK_4), .R_W(R_W_4), .Addr(Addr_4), .IN(IN_4), .OUT(OUT_4), .CLR(CLEAR_4));
  RAM_1x8 RAM_3 (.CLK(CLK_6), .R_W(R_W_6), .Addr(Addr_6), .IN(IN_7), .OUT(OUT_6), .CLR(CLEAR_6));
  RAM_4x8 RAM_4 (.CLK(CLK_2), .R_W(R_W_2), .Addr(Addr_2), .IN(IN_2), .OUT(OUT_2), .CLR(CLEAR_2));
  RAM_8x8 RAM_5 (.CLK(CLK_5), .R_W(R_W_5), .Addr(Addr_5), .IN(IN_5), .OUT(OUT_5), .CLR(CLEAR_5));
  RAM_1x16 RAM_6 (.CLK(CLK_7), .R_W(R_W_7), .Addr(Addr_7), .IN(IN_6), .OUT(OUT_7), .CLR(CLEAR_7));
  RAM_4x8 RAM_7 (.CLK(CLK_3), .R_W(R_W_3), .Addr(Addr_3), .IN(IN_3), .OUT(OUT_3), .CLR(CLEAR_3));

  // Notes on the sheet:
  //   Exemplo0081
  //   Exemplo0082
  //   Exemplo0083
  //   Exemplo0084
  //   Exemplo0085
  //   Exemplo0086
  //   Exemplo0087
endmodule

// 1x4
module RAM_1x4 (
  input  CLK,
  input  [3:0] IN,
  input  R_W,
  input  Addr,
  input  CLR,
  output [3:0] OUT
);

  wire and_1_out, not_1_out, not_2_out, not_3_out, not_4_out;
  wire [3:0] j_k_ff_4_q;

  and and_1 (and_1_out, CLK, R_W, Addr);
  J_K_Flip_Flop j_k_ff_1 (
    .J(IN[3]), .clk(and_1_out), .K(not_1_out), .Q(j_k_ff_4_q[3]), .reset(CLR));  // open: Qn, preset, en
  not not_1 (not_1_out, IN[3]);
  not not_2 (not_2_out, IN[2]);
  J_K_Flip_Flop j_k_ff_2 (
    .J(IN[2]), .clk(and_1_out), .K(not_2_out), .Q(j_k_ff_4_q[2]), .reset(CLR));  // open: Qn, preset, en
  J_K_Flip_Flop j_k_ff_3 (
    .J(IN[1]), .clk(and_1_out), .K(not_3_out), .Q(j_k_ff_4_q[1]), .reset(CLR));  // open: Qn, preset, en
  not not_3 (not_3_out, IN[1]);
  not not_4 (not_4_out, IN[0]);
  J_K_Flip_Flop j_k_ff_4 (
    .J(IN[0]), .clk(and_1_out), .K(not_4_out), .Q(j_k_ff_4_q[0]), .reset(CLR));  // open: Qn, preset, en
  assign OUT = j_k_ff_4_q & {4{Addr}};  // AND_Gate and_2, 4 bits wide
endmodule

// 2X4
module RAM_2x4 (
  input  CLK,
  input  R_W,
  input  Addr,
  input  [3:0] IN,
  input  CLR,
  output [3:0] OUT
);

  wire demultiplexer_1_out0, demultiplexer_1_out1;
  wire [3:0] ram_1x4_1_out, ram_1x4_2_out;

  Demultiplexer #(.enable("false")) demultiplexer_1 (
    .out0(demultiplexer_1_out0), .out1(demultiplexer_1_out1), .in(1'b1), .sel(Addr));
  RAM_1x4 ram_1x4_1 (.CLK(CLK), .R_W(R_W), .Addr(demultiplexer_1_out0), .IN(IN), .OUT(ram_1x4_1_out), .CLR(CLR));
  RAM_1x4 ram_1x4_2 (.CLK(CLK), .R_W(R_W), .Addr(demultiplexer_1_out1), .IN(IN), .OUT(ram_1x4_2_out), .CLR(CLR));
  Multiplexer #(.width(4), .enable("false")) multiplexer_1 (
    .in0(ram_1x4_1_out), .in1(ram_1x4_2_out), .out(OUT), .sel(Addr));
endmodule

// 1X8
module RAM_1x8 (
  input  CLK,
  input  R_W,
  input  Addr,
  input  [7:0] IN,
  input  CLR,
  output [7:0] OUT
);

  RAM_1x4 ram_1x4_1 (.CLK(CLK), .R_W(R_W), .Addr(Addr), .IN(IN[3:0]), .OUT(OUT[3:0]), .CLR(CLR));
  RAM_1x4 ram_1x4_2 (.CLK(CLK), .R_W(R_W), .Addr(Addr), .IN(IN[7:4]), .OUT(OUT[7:4]), .CLR(CLR));
endmodule

// 4X8
module RAM_4x8 (
  input  CLK,
  input  R_W,
  input  [1:0] Addr,
  input  [7:0] IN,
  input  CLR,
  output [7:0] OUT
);

  wire demultiplexer_1_out0, demultiplexer_1_out1, demultiplexer_1_out2, demultiplexer_1_out3;
  wire [7:0] ram_1x8_1_out, ram_1x8_2_out, ram_1x8_3_out, ram_1x8_4_out;

  Demultiplexer #(.select(2), .enable("false")) demultiplexer_1 (
    .out0(demultiplexer_1_out0), .out1(demultiplexer_1_out1), .out2(demultiplexer_1_out2),
    .out3(demultiplexer_1_out3), .in(1'b1), .sel(Addr));
  RAM_1x8 ram_1x8_1 (.CLK(CLK), .R_W(R_W), .Addr(demultiplexer_1_out0), .IN(IN), .OUT(ram_1x8_1_out), .CLR(CLR));
  RAM_1x8 ram_1x8_2 (.CLK(CLK), .R_W(R_W), .Addr(demultiplexer_1_out1), .IN(IN), .OUT(ram_1x8_2_out), .CLR(CLR));
  RAM_1x8 ram_1x8_3 (.CLK(CLK), .R_W(R_W), .Addr(demultiplexer_1_out2), .IN(IN), .OUT(ram_1x8_3_out), .CLR(CLR));
  RAM_1x8 ram_1x8_4 (.CLK(CLK), .R_W(R_W), .Addr(demultiplexer_1_out3), .IN(IN), .OUT(ram_1x8_4_out), .CLR(CLR));
  Multiplexer #(.select(2), .width(8), .enable("false")) multiplexer_1 (
    .in0(ram_1x8_1_out), .in1(ram_1x8_2_out), .in2(ram_1x8_3_out), .in3(ram_1x8_4_out), .out(OUT), .sel(Addr));
endmodule

// 8x8
module RAM_8x8 (
  input  CLK,
  input  R_W,
  input  [2:0] Addr,
  input  [7:0] IN,
  input  CLR,
  output [7:0] OUT
);

  wire [1:0] demultiplexer_1_out0, demultiplexer_1_out1, demultiplexer_1_out2, demultiplexer_1_out3,
       demultiplexer_1_out4, demultiplexer_1_out5, demultiplexer_1_out6, demultiplexer_1_out7;
  wire [7:0] ram_4x8_1_out, ram_4x8_2_out, ram_4x8_3_out, ram_4x8_4_out, ram_4x8_5_out, ram_4x8_6_out,
       ram_4x8_7_out, ram_4x8_8_out;

  Demultiplexer #(.select(3), .width(2), .enable("false")) demultiplexer_1 (
    .out0(demultiplexer_1_out0), .out1(demultiplexer_1_out1), .out2(demultiplexer_1_out2),
    .out3(demultiplexer_1_out3), .out4(demultiplexer_1_out4), .out5(demultiplexer_1_out5),
    .out6(demultiplexer_1_out6), .out7(demultiplexer_1_out7), .in(2'b01), .sel(Addr));
  RAM_4x8 ram_4x8_1 (.CLK(CLK), .R_W(R_W), .Addr(demultiplexer_1_out0), .IN(IN), .OUT(ram_4x8_1_out), .CLR(CLR));
  RAM_4x8 ram_4x8_2 (.CLK(CLK), .R_W(R_W), .Addr(demultiplexer_1_out1), .IN(IN), .OUT(ram_4x8_2_out), .CLR(CLR));
  RAM_4x8 ram_4x8_3 (.CLK(CLK), .R_W(R_W), .Addr(demultiplexer_1_out2), .IN(IN), .OUT(ram_4x8_3_out), .CLR(CLR));
  RAM_4x8 ram_4x8_4 (.CLK(CLK), .R_W(R_W), .Addr(demultiplexer_1_out3), .IN(IN), .OUT(ram_4x8_4_out), .CLR(CLR));
  RAM_4x8 ram_4x8_5 (.CLK(CLK), .R_W(R_W), .Addr(demultiplexer_1_out4), .IN(IN), .OUT(ram_4x8_5_out), .CLR(CLR));
  RAM_4x8 ram_4x8_6 (.CLK(CLK), .R_W(R_W), .Addr(demultiplexer_1_out5), .IN(IN), .OUT(ram_4x8_6_out), .CLR(CLR));
  RAM_4x8 ram_4x8_7 (.CLK(CLK), .R_W(R_W), .Addr(demultiplexer_1_out6), .IN(IN), .OUT(ram_4x8_7_out), .CLR(CLR));
  RAM_4x8 ram_4x8_8 (.CLK(CLK), .R_W(R_W), .Addr(demultiplexer_1_out7), .IN(IN), .OUT(ram_4x8_8_out), .CLR(CLR));
  Multiplexer #(.select(3), .width(8), .enable("false")) multiplexer_1 (
    .in0(ram_4x8_1_out), .in1(ram_4x8_2_out), .in2(ram_4x8_3_out), .in3(ram_4x8_4_out), .in4(ram_4x8_5_out),
    .in5(ram_4x8_6_out), .in6(ram_4x8_7_out), .in7(ram_4x8_8_out), .out(OUT), .sel(Addr));
endmodule

// 1X16
module RAM_1x16 (
  input  CLK,
  input  R_W,
  input  [15:0] IN,
  input  Addr,
  input  CLR,
  output [15:0] OUT
);

  RAM_1x8 ram_1x8_1 (.CLK(CLK), .R_W(R_W), .Addr(Addr), .IN(IN[7:0]), .OUT(OUT[7:0]), .CLR(CLR));
  RAM_1x8 ram_1x8_2 (.CLK(CLK), .R_W(R_W), .Addr(Addr), .IN(IN[15:8]), .OUT(OUT[15:8]), .CLR(CLR));
endmodule
