// Logisim project Exercicio04.circ as structural Verilog: 1 circuit, main circuit main
module main (
  input  _1,
  input  Pulse,
  input  CLR,
  output a,
  output b,
  output c,
  output d,
  output e
);

  wire j_k_ff_1_qn, j_k_ff_2_qn, j_k_ff_3_qn, j_k_ff_4_qn, nand_1_out, nand_2_out, not_1_out, not_2_out,
       not_3_out;

  nand nand_1 (nand_1_out, not_1_out, d, not_2_out, b, not_3_out);
  J_K_Flip_Flop j_k_ff_1 (
    .J(_1), .clk(Pulse), .K(_1), .Q(e), .Qn(j_k_ff_1_qn), .reset(nand_2_out));  // open: preset, en
  nand nand_2 (nand_2_out, CLR, nand_1_out);
  not not_1 (not_1_out, e);
  not not_2 (not_2_out, c);
  not not_3 (not_3_out, a);
  J_K_Flip_Flop j_k_ff_2 (
    .J(_1), .clk(j_k_ff_1_qn), .K(_1), .Q(d), .Qn(j_k_ff_2_qn), .reset(nand_2_out));  // open: preset, en
  J_K_Flip_Flop j_k_ff_3 (
    .J(_1), .clk(j_k_ff_2_qn), .K(_1), .Q(c), .Qn(j_k_ff_3_qn), .reset(nand_2_out));  // open: preset, en
  J_K_Flip_Flop j_k_ff_4 (
    .J(_1), .clk(j_k_ff_3_qn), .K(_1), .Q(b), .Qn(j_k_ff_4_qn), .reset(nand_2_out));  // open: preset, en
  J_K_Flip_Flop j_k_ff_5 (.J(_1), .clk(j_k_ff_4_qn), .K(_1), .Q(a), .reset(nand_2_out));  // open: Qn, preset, en
endmodule
