// Logisim project Circuitos.circ as structural Verilog
module Exercicio01 (
  input  Clock,
  input  [3:0] Entrada,
  input  Read___Write,
  input  Address,
  input  Clear,
  output [3:0] \Saída 
);

  RAM_1x4 ram_1x4_1 (
    .Clock(Clock), .Read___Write(Read___Write), .Address(Address), .Clear(Clear), .E(Entrada), .S(\Saída ));

  // Notes on the sheet:
  //   Exercicio01 - Djonatas Tulio Rodrigues Costa - 440954
  //   RAM 1x4
endmodule

module Exercicio02 (
  input  Clock,
  input  [3:0] Entrada,
  input  Read___Write,
  input  Address,
  input  Clear,
  output [3:0] \Saída 
);

  RAM_2x4 ram_2x4_1 (
    .Clock(Clock), .Read___Write(Read___Write), .Address(Address), .Clear(Clear), .Entrada(Entrada),
    .\Saída (\Saída ));

  // Notes on the sheet:
  //   Exercicio02 - Djonatas Tulio Rodrigues Costa - 440954
  //   RAM 2x4
endmodule

module Exercicio03 (
  input  Clock,
  input  [7:0] Entrada,
  input  Read___Write,
  input  Address,
  input  Clear,
  output [7:0] \Saída 
);

  RAM_1x8 ram_1x8_1 (
    .Clock(Clock), .Read___Write(Read___Write), .Address(Address), .Clear(Clear), .Entrada(Entrada),
    .\Saída (\Saída ));

  // Notes on the sheet:
  //   Exercicio03 - Djonatas Tulio Rodrigues Costa - 440954
  //   RAM 1x8
endmodule

module Exercicio04 (
  input  Clock,
  input  [7:0] Entrada,
  input  Read___Write,
  input  [1:0] Address,
  input  Clear,
  output [7:0] \Saída 
);

  RAM_2x8 ram_2x8_1 (
    .Clock(Clock), .Read___Write(Read___Write), .Address(Address), .Clear(Clear), .Entrada(Entrada),
    .\Saída (\Saída ));

  // Notes on the sheet:
  //   Exercicio04 - Djonatas Tulio Rodrigues Costa - 440954
  //   RAM 2x8
endmodule

module Exercicio05 (
  input  Clock,
  input  [7:0] Entrada,
  input  Read___Write,
  input  [2:0] Address,
  input  Clear,
  output [7:0] \Saída 
);

  RAM_8x8 ram_8x8_1 (
    .Clock(Clock), .Read___Write(Read___Write), .Address(Address), .Clear(Clear), .Entrada(Entrada),
    .\Saída (\Saída ));

  // Notes on the sheet:
  //   Exercicio05 - Djonatas Tulio Rodrigues Costa - 440954
  //   RAM 8x8
endmodule

// 1x4
module RAM_1x4 (
  input  [3:0] E,
  input  Clock,
  input  Read___Write,
  input  Address,
  input  Clear,
  output [3:0] S
);

  wire and_1_out, not_1_out, not_2_out, not_3_out, not_4_out;
  wire [3:0] j_k_ff_4_q;

  and and_1 (and_1_out, Clock, Read___Write, Address);
  J_K_Flip_Flop j_k_ff_1 (
    .J(E[3]), .clk(and_1_out), .K(not_1_out), .Q(j_k_ff_4_q[3]), .reset(Clear));  // open: Qn, preset, en
  not not_1 (not_1_out, E[3]);
  not not_2 (not_2_out, E[2]);
  J_K_Flip_Flop j_k_ff_2 (
    .J(E[2]), .clk(and_1_out), .K(not_2_out), .Q(j_k_ff_4_q[2]), .reset(Clear));  // open: Qn, preset, en
  not not_3 (not_3_out, E[1]);
  J_K_Flip_Flop j_k_ff_3 (
    .J(E[1]), .clk(and_1_out), .K(not_3_out), .Q(j_k_ff_4_q[1]), .reset(Clear));  // open: Qn, preset, en
  J_K_Flip_Flop j_k_ff_4 (
    .J(E[0]), .clk(and_1_out), .K(not_4_out), .Q(j_k_ff_4_q[0]), .reset(Clear));  // open: Qn, preset, en
  not not_4 (not_4_out, E[0]);
  assign S = j_k_ff_4_q & {4{Address}};  // AND_Gate and_2, 4 bits wide
endmodule

// 2x4
module RAM_2x4 (
  input  Clock,
  input  [3:0] Entrada,
  input  Read___Write,
  input  Address,
  input  Clear,
  output [3:0] \Saída 
);

  wire demultiplexer_1_out0, demultiplexer_1_out1;
  wire [3:0] ram_1x4_1_s, ram_1x4_2_s;

  Demultiplexer #(.enable("false")) demultiplexer_1 (
    .out0(demultiplexer_1_out0), .out1(demultiplexer_1_out1), .in(1'b1), .sel(Address));
  RAM_1x4 ram_1x4_1 (
    .Clock(Clock), .Read___Write(Read___Write), .Address(demultiplexer_1_out0), .Clear(Clear), .E(Entrada),
    .S(ram_1x4_1_s));
  RAM_1x4 ram_1x4_2 (
    .Clock(Clock), .Read___Write(Read___Write), .Address(demultiplexer_1_out1), .Clear(Clear), .E(Entrada),
    .S(ram_1x4_2_s));
  Multiplexer #(.width(4), .enable("false")) multiplexer_1 (
    .in0(ram_1x4_1_s), .in1(ram_1x4_2_s), .out(\Saída ), .sel(Address));
endmodule

// 1x8
module RAM_1x8 (
  input  Clock,
  input  [7:0] Entrada,
  input  Read___Write,
  input  Address,
  input  Clear,
  output [7:0] \Saída 
);

  RAM_1x4 ram_1x4_1 (
    .Clock(Clock), .Read___Write(Read___Write), .Address(Address), .Clear(Clear), .E(Entrada[3:0]),
    .S(\Saída [3:0]));
  RAM_1x4 ram_1x4_2 (
    .Clock(Clock), .Read___Write(Read___Write), .Address(Address), .Clear(Clear), .E(Entrada[7:4]),
    .S(\Saída [7:4]));
endmodule

// 2x8
module RAM_2x8 (
  input  [7:0] Entrada,
  input  Clock,
  input  Read___Write,
  input  [1:0] Address,
  input  Clear,
  output [7:0] \Saída 
);

  wire demultiplexer_1_out0, demultiplexer_1_out1, demultiplexer_1_out2, demultiplexer_1_out3;
  wire [3:0] \ram_2x4_1_saída , \ram_2x4_2_saída , \ram_2x4_3_saída , \ram_2x4_4_saída , \ram_2x4_5_saída ,
       \ram_2x4_6_saída , \ram_2x4_7_saída , \ram_2x4_8_saída ;

  Demultiplexer #(.select(2), .enable("false")) demultiplexer_1 (
    .out0(demultiplexer_1_out0), .out1(demultiplexer_1_out1), .out2(demultiplexer_1_out2),
    .out3(demultiplexer_1_out3), .in(1'b1), .sel(Address));
  RAM_2x4 ram_2x4_1 (
    .Clock(Clock), .Read___Write(Read___Write), .Address(demultiplexer_1_out0), .Clear(Clear),
    .Entrada(Entrada[3:0]), .\Saída (\ram_2x4_1_saída ));
  RAM_2x4 ram_2x4_2 (
    .Clock(Clock), .Read___Write(Read___Write), .Address(demultiplexer_1_out0), .Clear(Clear),
    .Entrada(Entrada[7:4]), .\Saída (\ram_2x4_2_saída ));
  RAM_2x4 ram_2x4_3 (
    .Clock(Clock), .Read___Write(Read___Write), .Address(demultiplexer_1_out1), .Clear(Clear),
    .Entrada(Entrada[3:0]), .\Saída (\ram_2x4_3_saída ));
  RAM_2x4 ram_2x4_4 (
    .Clock(Clock), .Read___Write(Read___Write), .Address(demultiplexer_1_out1), .Clear(Clear),
    .Entrada(Entrada[7:4]), .\Saída (\ram_2x4_4_saída ));
  RAM_2x4 ram_2x4_5 (
    .Clock(Clock), .Read___Write(Read___Write), .Address(demultiplexer_1_out2), .Clear(Clear),
    .Entrada(Entrada[3:0]), .\Saída (\ram_2x4_5_saída ));
  RAM_2x4 ram_2x4_6 (
    .Clock(Clock), .Read___Write(Read___Write), .Address(demultiplexer_1_out2), .Clear(Clear),
    .Entrada(Entrada[7:4]), .\Saída (\ram_2x4_6_saída ));
  RAM_2x4 ram_2x4_7 (
    .Clock(Clock), .Read___Write(Read___Write), .Address(demultiplexer_1_out3), .Clear(Clear),
    .Entrada(Entrada[3:0]), .\Saída (\ram_2x4_7_saída ));
  RAM_2x4 ram_2x4_8 (
    .Clock(Clock), .Read___Write(Read___Write), .Address(demultiplexer_1_out3), .Clear(Clear),
    .Entrada(Entrada[7:4]), .\Saída (\ram_2x4_8_saída ));
  Multiplexer #(.select(2), .width(8), .enable("false")) multiplexer_1 (
    .in0({\ram_2x4_2_saída , \ram_2x4_1_saída }), .in1({\ram_2x4_4_saída , \ram_2x4_3_saída }),
    .in2({\ram_2x4_6_saída , \ram_2x4_5_saída }), .in3({\ram_2x4_8_saída , \ram_2x4_7_saída }),
    .out(\Saída ), .sel(Address));
endmodule

// 8x8
module RAM_8x8 (
  input  [7:0] Entrada,
  input  Clock,
  input  Read___Write,
  input  [2:0] Address,
  input  Clear,
  output [7:0] \Saída 
);

  wire demultiplexer_1_out0, demultiplexer_1_out1, demultiplexer_1_out2, demultiplexer_1_out3,
       demultiplexer_1_out4, demultiplexer_1_out5, demultiplexer_1_out6, demultiplexer_1_out7;
  wire [7:0] \ram_1x8_1_saída , \ram_1x8_2_saída , \ram_1x8_3_saída , \ram_1x8_4_saída , \ram_1x8_5_saída ,
       \ram_1x8_6_saída , \ram_1x8_7_saída , \ram_1x8_8_saída ;

  Demultiplexer #(.select(3), .enable("false")) demultiplexer_1 (
    .out0(demultiplexer_1_out0), .out1(demultiplexer_1_out1), .out2(demultiplexer_1_out2),
    .out3(demultiplexer_1_out3), .out4(demultiplexer_1_out4), .out5(demultiplexer_1_out5),
    .out6(demultiplexer_1_out6), .out7(demultiplexer_1_out7), .in(1'b1), .sel(Address));
  RAM_1x8 ram_1x8_1 (
    .Clock(Clock), .Read___Write(Read___Write), .Address(demultiplexer_1_out0), .Clear(Clear),
    .Entrada(Entrada), .\Saída (\ram_1x8_1_saída ));
  RAM_1x8 ram_1x8_2 (
    .Clock(Clock), .Read___Write(Read___Write), .Address(demultiplexer_1_out1), .Clear(Clear),
    .Entrada(Entrada), .\Saída (\ram_1x8_2_saída ));
  RAM_1x8 ram_1x8_3 (
    .Clock(Clock), .Read___Write(Read___Write), .Address(demultiplexer_1_out2), .Clear(Clear),
    .Entrada(Entrada), .\Saída (\ram_1x8_3_saída ));
  RAM_1x8 ram_1x8_4 (
    .Clock(Clock), .Read___Write(Read___Write), .Address(demultiplexer_1_out3), .Clear(Clear),
    .Entrada(Entrada), .\Saída (\ram_1x8_4_saída ));
  RAM_1x8 ram_1x8_5 (
    .Clock(Clock), .Read___Write(Read___Write), .Address(demultiplexer_1_out4), .Clear(Clear),
    .Entrada(Entrada), .\Saída (\ram_1x8_5_saída ));
  RAM_1x8 ram_1x8_6 (
    .Clock(Clock), .Read___Write(Read___Write), .Address(demultiplexer_1_out5), .Clear(Clear),
    .Entrada(Entrada), .\Saída (\ram_1x8_6_saída ));
  RAM_1x8 ram_1x8_7 (
    .Clock(Clock), .Read___Write(Read___Write), .Address(demultiplexer_1_out6), .Clear(Clear),
    .Entrada(Entrada), .\Saída (\ram_1x8_7_saída ));
  RAM_1x8 ram_1x8_8 (
    .Clock(Clock), .Read___Write(Read___Write), .Address(demultiplexer_1_out7), .Clear(Clear),
    .Entrada(Entrada), .\Saída (\ram_1x8_8_saída ));
  Multiplexer #(.select(3), .width(8), .enable("false")) multiplexer_1 (
    .in0(\ram_1x8_5_saída ), .in1(\ram_1x8_6_saída ), .in2(\ram_1x8_7_saída ), .in3(\ram_1x8_8_saída ),
    .in4(\ram_1x8_1_saída ), .in5(\ram_1x8_2_saída ), .in6(\ram_1x8_3_saída ), .in7(\ram_1x8_4_saída ),
    .out(\Saída ), .sel(Address));
endmodule
