// Logisim project Exercicio03.circ as structural Verilog: 5 circuits, main circuit memoria 1x1
// 1x1
module memoria_1x1 (
  input  Addr,
  input  R_W,
  input  CLK,
  input  IN,
  input  CLR,
  output out_6
);

  wire and_1_out, j_k_ff_1_q, not_1_out;

  not not_1 (not_1_out, IN);
  and and_1 (and_1_out, Addr, R_W, CLK);
  J_K_Flip_Flop j_k_ff_1 (.J(IN), .clk(and_1_out), .K(not_1_out), .Q(j_k_ff_1_q), .reset(CLR));  // open: Qn, preset, en
  and and_2 (out_6, Addr, j_k_ff_1_q);
endmodule

// 1x2
module memoria_1x2 (
  input  Addr,
  input  R_W,
  input  CLK,
  input  IN0,
  input  IN1,
  input  CLR,
  output OUT0,
  output OUT1
);

  memoria_1x1 memoria_1x1_1 (.Addr(Addr), .R_W(R_W), .CLK(CLK), .IN(IN0), .CLR(CLR), .out_6(OUT0));
  memoria_1x1 memoria_1x1_2 (.Addr(Addr), .R_W(R_W), .CLK(CLK), .IN(IN1), .CLR(CLR), .out_6(OUT1));
endmodule

// 1x4
module memoria_1x4 (
  input  in_1,
  input  in_2,
  input  in_3,
  input  in_4,
  input  in_5,
  input  in_6,
  input  in_7,
  input  in_8,
  output out_9,
  output out_10,
  output out_11,
  output out_12
);

  memoria_1x2 memoria_1x2_1 (
    .Addr(in_1), .R_W(in_2), .CLK(in_3), .IN0(in_4), .IN1(in_5), .CLR(in_8), .OUT0(out_9), .OUT1(out_10));
  memoria_1x2 memoria_1x2_2 (
    .Addr(in_1), .R_W(in_2), .CLK(in_3), .IN0(in_6), .IN1(in_7), .CLR(in_8), .OUT0(out_11), .OUT1(out_12));
endmodule

module _2x4 (
  input  in_1,
  input  in_2,
  input  in_3,
  input  in_4,
  input  in_5,
  input  in_6,
  input  in_7,
  input  in_8,
  output [3:0] out_9
);

  wire demultiplexer_1_out0, demultiplexer_1_out1;
  wire [3:0] memoria_1x4_1_out_12, memoria_1x4_2_out_12;

  Demultiplexer demultiplexer_1 (
    .out0(demultiplexer_1_out0), .out1(demultiplexer_1_out1), .in(1'b1), .sel(in_1));  // open: en
  memoria_1x4 memoria_1x4_1 (
    .in_1(demultiplexer_1_out0), .in_2(in_2), .in_3(in_3), .in_4(in_4), .in_5(in_5), .in_6(in_6),
    .in_7(in_7), .in_8(in_8), .out_9(memoria_1x4_1_out_12[3]), .out_10(memoria_1x4_1_out_12[2]),
    .out_11(memoria_1x4_1_out_12[1]), .out_12(memoria_1x4_1_out_12[0]));
  memoria_1x4 memoria_1x4_2 (
    .in_1(demultiplexer_1_out1), .in_2(in_2), .in_3(in_3), .in_4(in_4), .in_5(in_5), .in_6(in_6),
    .in_7(in_7), .in_8(in_8), .out_9(memoria_1x4_2_out_12[3]), .out_10(memoria_1x4_2_out_12[2]),
    .out_11(memoria_1x4_2_out_12[1]), .out_12(memoria_1x4_2_out_12[0]));
  Multiplexer #(.width(4)) multiplexer_1 (
    .in0(memoria_1x4_1_out_12), .in1(memoria_1x4_2_out_12), .out(out_9), .sel(in_1));  // open: en
endmodule

module _1x8 (
  input  Addr,
  input  R_W,
  input  CLK,
  input  [7:0] IN,
  input  CLR,
  output [7:0] out_6
);

  memoria_1x4 memoria_1x4_1 (
    .in_1(Addr), .in_2(R_W), .in_3(CLK), .in_4(IN[7]), .in_5(IN[6]), .in_6(IN[5]), .in_7(IN[4]), .in_8(CLR),
    .out_9(out_6[7]), .out_10(out_6[6]), .out_11(out_6[5]), .out_12(out_6[4]));
  memoria_1x4 memoria_1x4_2 (
    .in_1(Addr), .in_2(R_W), .in_3(CLK), .in_4(IN[3]), .in_5(IN[2]), .in_6(IN[1]), .in_7(IN[0]), .in_8(CLR),
    .out_9(out_6[3]), .out_10(out_6[2]), .out_11(out_6[1]), .out_12(out_6[0]));
endmodule
