// Logisim project Exercicio05.circ as structural Verilog: 9 circuits, main circuit memoria 1x1
// 1x1
module memoria_1x1 (
  input  Addr,
  input  R_W,
  input  CLK,
  input  IN,
  input  CLR,
  output out_6
);

  wire and_1_out, j_k_ff_1_q, not_1_out;

  not not_1 (not_1_out, IN);
  and and_1 (and_1_out, Addr, R_W, CLK);
  J_K_Flip_Flop j_k_ff_1 (.J(IN), .clk(and_1_out), .K(not_1_out), .Q(j_k_ff_1_q), .reset(CLR));  // open: Qn, preset, en
  and and_2 (out_6, Addr, j_k_ff_1_q);
endmodule

// 1x2
module memoria_1x2 (
  input  Addr,
  input  R_W,
  input  CLK,
  input  IN0,
  input  IN1,
  input  CLR,
  output OUT0,
  output OUT1
);

  memoria_1x1 memoria_1x1_1 (.Addr(Addr), .R_W(R_W), .CLK(CLK), .IN(IN0), .CLR(CLR), .out_6(OUT0));
  memoria_1x1 memoria_1x1_2 (.Addr(Addr), .R_W(R_W), .CLK(CLK), .IN(IN1), .CLR(CLR), .out_6(OUT1));
endmodule

// 1x4
module memoria_1x4 (
  input  in_1,
  input  in_2,
  input  in_3,
  input  in_4,
  input  in_5,
  input  in_6,
  input  in_7,
  input  in_8,
  output out_9,
  output out_10,
  output out_11,
  output out_12
);

  memoria_1x2 memoria_1x2_1 (
    .Addr(in_1), .R_W(in_2), .CLK(in_3), .IN0(in_4), .IN1(in_5), .CLR(in_8), .OUT0(out_9), .OUT1(out_10));
  memoria_1x2 memoria_1x2_2 (
    .Addr(in_1), .R_W(in_2), .CLK(in_3), .IN0(in_6), .IN1(in_7), .CLR(in_8), .OUT0(out_11), .OUT1(out_12));
endmodule

module _2x4 (
  input  in_1,
  input  in_2,
  input  in_3,
  input  in_4,
  input  in_5,
  input  in_6,
  input  in_7,
  input  in_8,
  output [3:0] out_9
);

  wire demultiplexer_1_out0, demultiplexer_1_out1;
  wire [3:0] memoria_1x4_1_out_12, memoria_1x4_2_out_12;

  Demultiplexer demultiplexer_1 (
    .out0(demultiplexer_1_out0), .out1(demultiplexer_1_out1), .in(1'b1), .sel(in_1));  // open: en
  memoria_1x4 memoria_1x4_1 (
    .in_1(demultiplexer_1_out0), .in_2(in_2), .in_3(in_3), .in_4(in_4), .in_5(in_5), .in_6(in_6),
    .in_7(in_7), .in_8(in_8), .out_9(memoria_1x4_1_out_12[3]), .out_10(memoria_1x4_1_out_12[2]),
    .out_11(memoria_1x4_1_out_12[1]), .out_12(memoria_1x4_1_out_12[0]));
  memoria_1x4 memoria_1x4_2 (
    .in_1(demultiplexer_1_out1), .in_2(in_2), .in_3(in_3), .in_4(in_4), .in_5(in_5), .in_6(in_6),
    .in_7(in_7), .in_8(in_8), .out_9(memoria_1x4_2_out_12[3]), .out_10(memoria_1x4_2_out_12[2]),
    .out_11(memoria_1x4_2_out_12[1]), .out_12(memoria_1x4_2_out_12[0]));
  Multiplexer #(.width(4)) multiplexer_1 (
    .in0(memoria_1x4_1_out_12), .in1(memoria_1x4_2_out_12), .out(out_9), .sel(in_1));  // open: en
endmodule

module _1x8 (
  input  Addr,
  input  R_W,
  input  CLK,
  input  [7:0] IN,
  input  CLR,
  output [7:0] out_6
);

  memoria_1x4 memoria_1x4_1 (
    .in_1(Addr), .in_2(R_W), .in_3(CLK), .in_4(IN[7]), .in_5(IN[6]), .in_6(IN[5]), .in_7(IN[4]), .in_8(CLR),
    .out_9(out_6[7]), .out_10(out_6[6]), .out_11(out_6[5]), .out_12(out_6[4]));
  memoria_1x4 memoria_1x4_2 (
    .in_1(Addr), .in_2(R_W), .in_3(CLK), .in_4(IN[3]), .in_5(IN[2]), .in_6(IN[1]), .in_7(IN[0]), .in_8(CLR),
    .out_9(out_6[3]), .out_10(out_6[2]), .out_11(out_6[1]), .out_12(out_6[0]));
endmodule

module _2x8 (
  input  Addr,
  input  R_W,
  input  CLK,
  input  [7:0] IN,
  input  CLR,
  output [7:0] out_6
);

  wire demultiplexer_1_out0, demultiplexer_1_out1;
  wire [3:0] n2x4_1_out_9, n2x4_2_out_9, n2x4_3_out_9, n2x4_4_out_9;

  Demultiplexer demultiplexer_1 (
    .out0(demultiplexer_1_out0), .out1(demultiplexer_1_out1), .in(1'b1), .sel(Addr));  // open: en
  _2x4 u_2x4_1 (
    .in_1(demultiplexer_1_out0), .in_2(R_W), .in_3(CLK), .in_4(IN[7]), .in_5(IN[6]), .in_6(IN[5]),
    .in_7(IN[4]), .in_8(CLR), .out_9(n2x4_1_out_9));
  _2x4 u_2x4_2 (
    .in_1(demultiplexer_1_out0), .in_2(R_W), .in_3(CLK), .in_4(IN[3]), .in_5(IN[2]), .in_6(IN[1]),
    .in_7(IN[0]), .in_8(CLR), .out_9(n2x4_2_out_9));
  _2x4 u_2x4_3 (
    .in_1(demultiplexer_1_out1), .in_2(R_W), .in_3(CLK), .in_4(IN[7]), .in_5(IN[6]), .in_6(IN[5]),
    .in_7(IN[4]), .in_8(CLR), .out_9(n2x4_3_out_9));
  _2x4 u_2x4_4 (
    .in_1(demultiplexer_1_out1), .in_2(R_W), .in_3(CLK), .in_4(IN[3]), .in_5(IN[2]), .in_6(IN[1]),
    .in_7(IN[0]), .in_8(CLR), .out_9(n2x4_4_out_9));
  Multiplexer #(.width(8)) multiplexer_1 (
    .in0({n2x4_1_out_9, n2x4_2_out_9}), .in1({n2x4_3_out_9, n2x4_4_out_9}), .out(out_6), .sel(Addr));  // open: en
endmodule

module _8x8 (
  input  [2:0] Addr,
  input  R_W,
  input  CLK,
  input  [7:0] IN,
  input  CLR,
  output [7:0] out_6
);

  wire and_1_out, and_2_out, and_3_out, and_4_out, demultiplexer_1_out0, demultiplexer_1_out1,
       demultiplexer_1_out2, demultiplexer_1_out3, demultiplexer_1_out4, demultiplexer_1_out5,
       demultiplexer_1_out6, demultiplexer_1_out7, or_1_out, or_2_out, or_3_out, or_4_out;
  wire [7:0] n2x8_1_out_6, n2x8_2_out_6, n2x8_3_out_6, n2x8_4_out_6;

  or or_1 (or_1_out, demultiplexer_1_out0, demultiplexer_1_out1);
  Demultiplexer #(.select(3)) demultiplexer_1 (
    .out0(demultiplexer_1_out0), .out1(demultiplexer_1_out1), .out2(demultiplexer_1_out2),
    .out3(demultiplexer_1_out3), .out4(demultiplexer_1_out4), .out5(demultiplexer_1_out5),
    .out6(demultiplexer_1_out6), .out7(demultiplexer_1_out7), .in(1'b1), .sel(Addr));  // open: en
  and and_1 (and_1_out, or_1_out, R_W);
  or or_2 (or_2_out, demultiplexer_1_out2, demultiplexer_1_out3);
  or or_3 (or_3_out, demultiplexer_1_out4, demultiplexer_1_out5);
  or or_4 (or_4_out, demultiplexer_1_out6, demultiplexer_1_out7);
  and and_2 (and_2_out, or_2_out, R_W);
  _2x8 u_2x8_1 (.Addr(demultiplexer_1_out0), .R_W(and_1_out), .CLK(CLK), .IN(IN), .CLR(CLR), .out_6(n2x8_1_out_6));
  and and_3 (and_3_out, or_3_out, R_W);
  _2x8 u_2x8_2 (.Addr(demultiplexer_1_out2), .R_W(and_2_out), .CLK(CLK), .IN(IN), .CLR(CLR), .out_6(n2x8_2_out_6));
  and and_4 (and_4_out, or_4_out, R_W);
  _2x8 u_2x8_3 (.Addr(demultiplexer_1_out4), .R_W(and_3_out), .CLK(CLK), .IN(IN), .CLR(CLR), .out_6(n2x8_3_out_6));
  _2x8 u_2x8_4 (.Addr(demultiplexer_1_out6), .R_W(and_4_out), .CLK(CLK), .IN(IN), .CLR(CLR), .out_6(n2x8_4_out_6));
  Multiplexer #(.select(3), .width(8)) multiplexer_1 (
    .in0(n2x8_1_out_6), .in1(n2x8_1_out_6), .in2(n2x8_2_out_6), .in3(n2x8_2_out_6), .in4(n2x8_3_out_6),
    .in5(n2x8_3_out_6), .in6(n2x8_4_out_6), .in7(n2x8_4_out_6), .out(out_6), .sel(Addr));  // open: en
endmodule

module _4x8 (
  input  [1:0] Addr,
  input  R_W,
  input  CLK,
  input  [7:0] IN,
  input  CLR,
  output [7:0] out_6
);

  wire demultiplexer_1_out0, demultiplexer_1_out1, demultiplexer_1_out2, demultiplexer_1_out3;
  wire [3:0] memoria_1x4_1_out_9, memoria_1x4_2_out_9, memoria_1x4_3_out_9, memoria_1x4_4_out_9,
       memoria_1x4_5_out_9, memoria_1x4_6_out_9, memoria_1x4_7_out_9, memoria_1x4_8_out_9;

  Demultiplexer #(.select(2)) demultiplexer_1 (
    .out0(demultiplexer_1_out0), .out1(demultiplexer_1_out1), .out2(demultiplexer_1_out2),
    .out3(demultiplexer_1_out3), .in(1'b1), .sel(Addr));  // open: en
  memoria_1x4 memoria_1x4_1 (
    .in_1(demultiplexer_1_out0), .in_2(R_W), .in_3(CLK), .in_4(IN[4]), .in_5(IN[5]), .in_6(IN[6]),
    .in_7(IN[7]), .in_8(CLR), .out_9(memoria_1x4_1_out_9[0]), .out_10(memoria_1x4_1_out_9[1]),
    .out_11(memoria_1x4_1_out_9[2]), .out_12(memoria_1x4_1_out_9[3]));
  memoria_1x4 memoria_1x4_2 (
    .in_1(demultiplexer_1_out2), .in_2(R_W), .in_3(CLK), .in_4(IN[4]), .in_5(IN[5]), .in_6(IN[6]),
    .in_7(IN[7]), .in_8(CLR), .out_9(memoria_1x4_2_out_9[0]), .out_10(memoria_1x4_2_out_9[1]),
    .out_11(memoria_1x4_2_out_9[2]), .out_12(memoria_1x4_2_out_9[3]));
  memoria_1x4 memoria_1x4_3 (
    .in_1(demultiplexer_1_out0), .in_2(R_W), .in_3(CLK), .in_4(IN[0]), .in_5(IN[1]), .in_6(IN[2]),
    .in_7(IN[3]), .in_8(CLR), .out_9(memoria_1x4_3_out_9[0]), .out_10(memoria_1x4_3_out_9[1]),
    .out_11(memoria_1x4_3_out_9[2]), .out_12(memoria_1x4_3_out_9[3]));
  memoria_1x4 memoria_1x4_4 (
    .in_1(demultiplexer_1_out2), .in_2(R_W), .in_3(CLK), .in_4(IN[0]), .in_5(IN[1]), .in_6(IN[2]),
    .in_7(IN[3]), .in_8(CLR), .out_9(memoria_1x4_4_out_9[0]), .out_10(memoria_1x4_4_out_9[1]),
    .out_11(memoria_1x4_4_out_9[2]), .out_12(memoria_1x4_4_out_9[3]));
  memoria_1x4 memoria_1x4_5 (
    .in_1(demultiplexer_1_out1), .in_2(R_W), .in_3(CLK), .in_4(IN[7]), .in_5(IN[6]), .in_6(IN[5]),
    .in_7(IN[4]), .in_8(CLR), .out_9(memoria_1x4_5_out_9[0]), .out_10(memoria_1x4_5_out_9[1]),
    .out_11(memoria_1x4_5_out_9[2]), .out_12(memoria_1x4_5_out_9[3]));
  memoria_1x4 memoria_1x4_6 (
    .in_1(demultiplexer_1_out3), .in_2(R_W), .in_3(CLK), .in_4(IN[7]), .in_5(IN[6]), .in_6(IN[5]),
    .in_7(IN[4]), .in_8(CLR), .out_9(memoria_1x4_6_out_9[0]), .out_10(memoria_1x4_6_out_9[1]),
    .out_11(memoria_1x4_6_out_9[2]), .out_12(memoria_1x4_6_out_9[3]));
  memoria_1x4 memoria_1x4_7 (
    .in_1(demultiplexer_1_out1), .in_2(R_W), .in_3(CLK), .in_4(IN[0]), .in_5(IN[1]), .in_6(IN[2]),
    .in_7(IN[3]), .in_8(CLR), .out_9(memoria_1x4_7_out_9[0]), .out_10(memoria_1x4_7_out_9[1]),
    .out_11(memoria_1x4_7_out_9[2]), .out_12(memoria_1x4_7_out_9[3]));
  memoria_1x4 memoria_1x4_8 (
    .in_1(demultiplexer_1_out3), .in_2(R_W), .in_3(CLK), .in_4(IN[0]), .in_5(IN[1]), .in_6(IN[2]),
    .in_7(IN[3]), .in_8(CLR), .out_9(memoria_1x4_8_out_9[0]), .out_10(memoria_1x4_8_out_9[1]),
    .out_11(memoria_1x4_8_out_9[2]), .out_12(memoria_1x4_8_out_9[3]));
  Multiplexer #(.select(2), .width(8)) multiplexer_1 (
    .in0({memoria_1x4_1_out_9, memoria_1x4_3_out_9}), .in1({memoria_1x4_5_out_9, memoria_1x4_7_out_9}),
    .in2({memoria_1x4_2_out_9, memoria_1x4_4_out_9}), .in3({memoria_1x4_6_out_9, memoria_1x4_8_out_9}),
    .out(out_6), .sel(Addr));  // open: en
endmodule

module _8x8_portas_4x8 (
  input  [2:0] Addr,
  input  R_W,
  input  CLK,
  input  [7:0] IN,
  input  CLR,
  output [7:0] out_6
);

  wire and_1_out, and_2_out, not_1_out;
  wire [7:0] n4x8_1_out_6, n4x8_2_out_6;

  not not_1 (not_1_out, Addr[2]);
  and and_1 (and_1_out, not_1_out, R_W);
  and and_2 (and_2_out, Addr[2], R_W);
  _4x8 u_4x8_1 (.Addr(Addr[1:0]), .R_W(and_1_out), .CLK(CLK), .IN(IN), .CLR(CLR), .out_6(n4x8_1_out_6));
  _4x8 u_4x8_2 (.Addr(Addr[1:0]), .R_W(and_2_out), .CLK(CLK), .IN(IN), .CLR(CLR), .out_6(n4x8_2_out_6));
  Multiplexer #(.width(8)) multiplexer_1 (
    .in0(n4x8_1_out_6), .in1(n4x8_2_out_6), .out(out_6), .sel(Addr[2]));  // open: en
endmodule
