// Logisim project Circuito_Guia10.circ as structural Verilog
// 4x1
module Exercicio01 (
  input  Clock,
  input  [3:0] INPUT,
  input  R___W,
  input  ADDR,
  input  Clear,
  output [3:0] OUTPUT
);

  wire and_1_out, not_1_out, not_2_out, not_3_out, not_4_out;
  wire [3:0] j_k_ff_4_q;

  and and_1 (and_1_out, Clock, R___W, ADDR);
  not not_1 (not_1_out, INPUT[3]);
  J_K_Flip_Flop j_k_ff_1 (
    .J(INPUT[3]), .clk(and_1_out), .K(not_1_out), .Q(j_k_ff_4_q[3]), .reset(Clear));  // open: Qn, preset, en
  J_K_Flip_Flop j_k_ff_2 (
    .J(INPUT[2]), .clk(and_1_out), .K(not_2_out), .Q(j_k_ff_4_q[2]), .reset(Clear));  // open: Qn, preset, en
  not not_2 (not_2_out, INPUT[2]);
  not not_3 (not_3_out, INPUT[1]);
  J_K_Flip_Flop j_k_ff_3 (
    .J(INPUT[1]), .clk(and_1_out), .K(not_3_out), .Q(j_k_ff_4_q[1]), .reset(Clear));  // open: Qn, preset, en
  J_K_Flip_Flop j_k_ff_4 (
    .J(INPUT[0]), .clk(and_1_out), .K(not_4_out), .Q(j_k_ff_4_q[0]), .reset(Clear));  // open: Qn, preset, en
  not not_4 (not_4_out, INPUT[0]);
  assign OUTPUT = j_k_ff_4_q & {4{ADDR}};  // AND_Gate and_2, 4 bits wide

  // Notes on the sheet:
  //   W
endmodule

// 2x4
module Exercicio02 (
  input  Clock,
  input  [3:0] INPUT,
  input  R___W,
  input  ADDR,
  input  Clear,
  output [3:0] OUTPUT
);

  wire demultiplexer_1_out0, demultiplexer_1_out1;
  wire [3:0] exercicio01_1_output, exercicio01_2_output;

  Demultiplexer #(.enable("false")) demultiplexer_1 (
    .out0(demultiplexer_1_out0), .out1(demultiplexer_1_out1), .in(1'b1), .sel(ADDR));
  Exercicio01 exercicio01_1 (
    .Clock(Clock), .R___W(R___W), .ADDR(demultiplexer_1_out0), .Clear(Clear), .INPUT(INPUT),
    .OUTPUT(exercicio01_1_output));
  Exercicio01 exercicio01_2 (
    .Clock(Clock), .R___W(R___W), .ADDR(demultiplexer_1_out1), .Clear(Clear), .INPUT(INPUT),
    .OUTPUT(exercicio01_2_output));
  Multiplexer #(.width(4), .enable("false")) multiplexer_1 (
    .in0(exercicio01_1_output), .in1(exercicio01_2_output), .out(OUTPUT), .sel(ADDR));
endmodule

// 1x8
module Exercicio03 (
  input  Clock,
  input  [7:0] INPUT,
  input  R___W,
  input  ADDR,
  input  Clear,
  output [7:0] OUTPUT
);

  Exercicio01 exercicio01_1 (
    .Clock(Clock), .R___W(R___W), .ADDR(ADDR), .Clear(Clear), .INPUT(INPUT[3:0]), .OUTPUT(OUTPUT[3:0]));
  Exercicio01 exercicio01_2 (
    .Clock(Clock), .R___W(R___W), .ADDR(ADDR), .Clear(Clear), .INPUT(INPUT[7:4]), .OUTPUT(OUTPUT[7:4]));
endmodule

// 2X8
module Exercicio04 (
  input  Clock,
  input  [7:0] INPUT,
  input  R___W,
  input  ADDR,
  input  Clear,
  output [7:0] OUTPUT
);

  Exercicio02 exercicio02_1 (
    .Clock(Clock), .R___W(R___W), .ADDR(ADDR), .Clear(Clear), .INPUT(INPUT[3:0]), .OUTPUT(OUTPUT[3:0]));
  Exercicio02 exercicio02_2 (
    .Clock(Clock), .R___W(R___W), .ADDR(ADDR), .Clear(Clear), .INPUT(INPUT[7:4]), .OUTPUT(OUTPUT[7:4]));
endmodule

module Exercicio05 (
  input  [2:0] ADDR,
  input  Clock,
  input  [7:0] INPUT,
  input  R___W,
  input  Clock_2,
  output [7:0] OUTPUT
);

  wire and_1_out, and_2_out, and_3_out, and_4_out, demultiplexer_1_out0, demultiplexer_1_out1,
       demultiplexer_1_out2, demultiplexer_1_out3;
  wire [7:0] exercicio04_1_output, exercicio04_2_output, exercicio04_3_output, exercicio04_4_output;

  Demultiplexer #(.select(2), .enable("false")) demultiplexer_1 (
    .out0(demultiplexer_1_out0), .out1(demultiplexer_1_out1), .out2(demultiplexer_1_out2),
    .out3(demultiplexer_1_out3), .in(1'b1), .sel(ADDR[1:0]));
  and and_1 (and_1_out, demultiplexer_1_out0, ADDR[2]);
  and and_2 (and_2_out, demultiplexer_1_out1, ADDR[2]);
  and and_3 (and_3_out, demultiplexer_1_out2, ADDR[2]);
  and and_4 (and_4_out, demultiplexer_1_out3, ADDR[2]);
  Exercicio04 exercicio04_1 (
    .Clock(Clock), .R___W(R___W), .ADDR(and_1_out), .Clear(Clock_2), .INPUT(INPUT),
    .OUTPUT(exercicio04_1_output));
  Exercicio04 exercicio04_2 (
    .Clock(Clock), .R___W(R___W), .ADDR(and_2_out), .Clear(Clock_2), .INPUT(INPUT),
    .OUTPUT(exercicio04_2_output));
  Exercicio04 exercicio04_3 (
    .Clock(Clock), .R___W(R___W), .ADDR(and_3_out), .Clear(Clock_2), .INPUT(INPUT),
    .OUTPUT(exercicio04_3_output));
  Exercicio04 exercicio04_4 (
    .Clock(Clock), .R___W(R___W), .ADDR(and_4_out), .Clear(Clock_2), .INPUT(INPUT),
    .OUTPUT(exercicio04_4_output));
  Multiplexer #(.select(2), .width(8), .enable("false")) multiplexer_1 (
    .in0(exercicio04_1_output), .in1(exercicio04_2_output), .in2(exercicio04_3_output),
    .in3(exercicio04_4_output), .out(OUTPUT), .sel(ADDR[1:0]));
endmodule

module Exercicio06 (
  input  Clock,
  input  [15:0] INPUT,
  input  R___W,
  input  ADDR,
  input  Clear,
  output [15:0] OUTPUT
);

  Exercicio03 exercicio03_1 (
    .Clock(Clock), .R___W(R___W), .ADDR(ADDR), .Clear(Clear), .INPUT(INPUT[7:0]), .OUTPUT(OUTPUT[7:0]));
  Exercicio03 exercicio03_2 (
    .Clock(Clock), .R___W(R___W), .ADDR(ADDR), .Clear(Clear), .INPUT(INPUT[15:8]), .OUTPUT(OUTPUT[15:8]));
endmodule

module Exercicio07 (
  input  [1:0] ADDR,
  input  Clock,
  input  [7:0] INPUT,
  input  R___W,
  input  Clock_2,
  output [7:0] OUTPUT
);

  wire demultiplexer_1_out0, demultiplexer_1_out1, demultiplexer_1_out2, demultiplexer_1_out3;
  wire [7:0] exercicio03_1_output, exercicio03_2_output, exercicio03_3_output, exercicio03_4_output;

  Demultiplexer #(.select(2), .enable("false")) demultiplexer_1 (
    .out0(demultiplexer_1_out0), .out1(demultiplexer_1_out1), .out2(demultiplexer_1_out2),
    .out3(demultiplexer_1_out3), .in(1'b1), .sel(ADDR));
  Exercicio03 exercicio03_1 (
    .Clock(Clock), .R___W(R___W), .ADDR(demultiplexer_1_out0), .Clear(Clock_2), .INPUT(INPUT),
    .OUTPUT(exercicio03_1_output));
  Exercicio03 exercicio03_2 (
    .Clock(Clock), .R___W(R___W), .ADDR(demultiplexer_1_out1), .Clear(Clock_2), .INPUT(INPUT),
    .OUTPUT(exercicio03_2_output));
  Exercicio03 exercicio03_3 (
    .Clock(Clock), .R___W(R___W), .ADDR(demultiplexer_1_out2), .Clear(Clock_2), .INPUT(INPUT),
    .OUTPUT(exercicio03_3_output));
  Exercicio03 exercicio03_4 (
    .Clock(Clock), .R___W(R___W), .ADDR(demultiplexer_1_out3), .Clear(Clock_2), .INPUT(INPUT),
    .OUTPUT(exercicio03_4_output));
  Multiplexer #(.select(2), .width(8), .enable("false")) multiplexer_1 (
    .in0(exercicio03_1_output), .in1(exercicio03_2_output), .in2(exercicio03_3_output),
    .in3(exercicio03_4_output), .out(OUTPUT), .sel(ADDR));
endmodule
