// Logisim project Projeto de circuito do Exemplo0071.circ as structural Verilog: 3 circuits, main circuit Memória RAM 1X1
// 1X1
module \Memória_RAM_1X1  (
  input  CLK,
  input  ADDR,
  input  R_W,
  input  IN,
  input  CLR,
  output OUT
);

  wire and_1_out, j_k_ff_1_q, or_1_out;

  and and_1 (and_1_out, CLK, ADDR, R_W);
  or or_1 (or_1_out, R_W, IN);
  J_K_Flip_Flop j_k_ff_1 (
    .J(or_1_out), .clk(and_1_out), .K(or_1_out), .Q(j_k_ff_1_q), .reset(CLR));  // open: Qn, preset, en
  and and_2 (OUT, ADDR, j_k_ff_1_q);

  // Notes on the sheet:
  //   Matrícula: 448662
  //   Nome: Josemar Alves Caetano
endmodule

// 1x4
module \Memória_RAM_1x4  (
  input  CLK,
  input  ADDR,
  input  R_W,
  input  IN,
  input  CLR,
  output [3:0] OUT
);

  \Memória_RAM_1X1  \memória_ram_1x1_1  (.CLK(CLK), .ADDR(ADDR), .R_W(R_W), .IN(IN), .CLR(CLR), .OUT(OUT[0]));
  \Memória_RAM_1X1  \memória_ram_1x1_2  (.CLK(CLK), .ADDR(ADDR), .R_W(R_W), .IN(IN), .CLR(CLR), .OUT(OUT[1]));
  \Memória_RAM_1X1  \memória_ram_1x1_3  (.CLK(CLK), .ADDR(ADDR), .R_W(R_W), .IN(IN), .CLR(CLR), .OUT(OUT[2]));
  \Memória_RAM_1X1  \memória_ram_1x1_4  (.CLK(CLK), .ADDR(ADDR), .R_W(R_W), .IN(IN), .CLR(CLR), .OUT(OUT[3]));

  // Notes on the sheet:
  //   Matrícula: 448662
  //   Nome: Josemar Alves Caetano
endmodule

module Exemplo0071 (
  input  CLK,
  input  ADDR,
  input  R_W,
  input  IN,
  input  CLR,
  output [3:0] OUT
);

  \Memória_RAM_1x4  \memória_ram_1x4_1  (.CLK(CLK), .ADDR(ADDR), .R_W(R_W), .IN(IN), .CLR(CLR), .OUT(OUT));

  // Notes on the sheet:
  //   Matrícula: 448662
  //   Nome: Josemar Alves Caetano
endmodule
