// Logisim project Projeto de circuito do Exemplo0072.circ as structural Verilog: 2 circuits, main circuit Exemplo0072
// 2x4
module \Memória_RAM_2x4  (
  input  CLK,
  input  [1:0] ADDR,
  input  R_W,
  input  IN,
  input  CLR,
  output [3:0] OUT_0,
  output [3:0] OUT_1
);

  \Memória_RAM_1x4  \memória_ram_1x4_1  (.CLK(CLK), .ADDR(ADDR[1]), .R_W(R_W), .IN(IN), .CLR(CLR), .OUT(OUT_0));
  \Memória_RAM_1x4  \memória_ram_1x4_2  (.CLK(CLK), .ADDR(ADDR[0]), .R_W(R_W), .IN(IN), .CLR(CLR), .OUT(OUT_1));

  // Notes on the sheet:
  //   Matrícula: 448662
  //   Nome: Josemar Alves Caetano
endmodule

module Exemplo0072 (
  input  [1:0] ADDR,
  input  R_W,
  input  IN,
  input  CLR,
  output [3:0] OUT_0,
  output [3:0] OUT_1
);

  wire clock_1_out;

  Clock clock_1 (.out(clock_1_out));
  \Memória_RAM_2x4  \memória_ram_2x4_1  (
    .CLK(clock_1_out), .ADDR(ADDR), .R_W(R_W), .IN(IN), .CLR(CLR), .OUT_0(OUT_0), .OUT_1(OUT_1));

  // Notes on the sheet:
  //   Matrícula: 448662
  //   Nome: Josemar Alves Caetano
endmodule
