// Logisim project Projeto de circuito do Exemplo0073.circ as structural Verilog: 2 circuits, main circuit Exemplo0073
// 1x8
module \Memória_RAM_1x8  (
  input  CLK,
  input  ADDR,
  input  R_W,
  input  IN,
  input  CLR,
  output [7:0] OUT
);

  \Memória_RAM_1x4  \memória_ram_1x4_1  (.CLK(CLK), .ADDR(ADDR), .R_W(R_W), .IN(IN), .CLR(CLR), .OUT(OUT[3:0]));
  \Memória_RAM_1x4  \memória_ram_1x4_2  (.CLK(CLK), .ADDR(ADDR), .R_W(R_W), .IN(IN), .CLR(CLR), .OUT(OUT[7:4]));

  // Notes on the sheet:
  //   Matrícula: 448662
  //   Nome: Josemar Alves Caetano
endmodule

module Exemplo0073 (
  input  ADDR,
  input  R_W,
  input  IN,
  input  CLR,
  output [7:0] OUT
);

  wire clock_1_out;

  Clock clock_1 (.out(clock_1_out));
  \Memória_RAM_1x8  \memória_ram_1x8_1  (.CLK(clock_1_out), .ADDR(ADDR), .R_W(R_W), .IN(IN), .CLR(CLR), .OUT(OUT));

  // Notes on the sheet:
  //   Matrícula: 448662
  //   Nome: Josemar Alves Caetano
endmodule
