// Logisim project Projeto de circuito do Exemplo0074.circ as structural Verilog: 3 circuits, main circuit Exemplo0074
module Exemplo0074 (
  input  [1:0] ADDR,
  input  R_W,
  input  IN,
  input  CLR,
  output [7:0] OUT
);

  wire CLK_out;

  Clock CLK (.out(CLK_out));
  \Memória_RAM_2x8  \memória_ram_2x8_1  (.CLK(CLK_out), .ADDR(ADDR), .R_W(R_W), .IN(IN), .CLR(CLR), .OUT(OUT));

  // Notes on the sheet:
  //   Matrícula: 448662
  //   Nome: Josemar Alves Caetano
endmodule

// 2x4
module \Memória_RAM_2x4  (
  input  CLK,
  input  ADDR,
  input  R_W,
  input  IN,
  input  CLR,
  output [3:0] OUT
);

  \Memória_RAM_1x4  \memória_ram_1x4_1  (.CLK(CLK), .ADDR(ADDR), .R_W(R_W), .IN(IN), .CLR(CLR), .OUT(OUT));

  // Notes on the sheet:
  //   Matrícula: 448662
  //   Nome: Josemar Alves Caetano
endmodule

// 2x8
module \Memória_RAM_2x8  (
  input  CLK,
  input  [1:0] ADDR,
  input  R_W,
  input  IN,
  input  CLR,
  output [7:0] OUT
);

  \Memória_RAM_2x4  \memória_ram_2x4_1  (.CLK(CLK), .ADDR(ADDR[1]), .R_W(R_W), .IN(IN), .CLR(CLR), .OUT(OUT[3:0]));
  \Memória_RAM_2x4  \memória_ram_2x4_2  (.CLK(CLK), .ADDR(ADDR[0]), .R_W(R_W), .IN(IN), .CLR(CLR), .OUT(OUT[7:4]));

  // Notes on the sheet:
  //   Matrícula: 448662
  //   Nome: Josemar Alves Caetano
endmodule
