// Logisim project Projeto de circuito do Exemplo0075.circ as structural Verilog: 2 circuits, main circuit Exemplo0075
// 8x8
module \Memória_RAM_8x8  (
  input  CLK,
  input  [3:0] ADDR,
  input  R_W,
  input  IN,
  input  CLR,
  output [7:0] OUT_0,
  output [7:0] OUT_1
);

  \Memória_RAM_2x8  \memória_ram_2x8_1  (.CLK(CLK), .ADDR(ADDR[1:0]), .R_W(R_W), .IN(IN), .CLR(CLR), .OUT(OUT_0));
  \Memória_RAM_2x8  \memória_ram_2x8_2  (.CLK(CLK), .ADDR(ADDR[3:2]), .R_W(R_W), .IN(IN), .CLR(CLR), .OUT(OUT_1));

  // Notes on the sheet:
  //   Matrícula: 448662
  //   Nome: Josemar Alves Caetano
endmodule

module Exemplo0075 (
  input  [3:0] ADDR,
  input  R_W,
  input  IN,
  input  CLR,
  output [7:0] OUT_0,
  output [7:0] OUT_1
);

  wire clock_1_out;

  Clock clock_1 (.out(clock_1_out));
  \Memória_RAM_8x8  \memória_ram_8x8_1  (
    .CLK(clock_1_out), .ADDR(ADDR), .R_W(R_W), .IN(IN), .CLR(CLR), .OUT_0(OUT_0), .OUT_1(OUT_1));

  // Notes on the sheet:
  //   Matrícula: 448662
  //   Nome: Josemar Alves Caetano
endmodule
