// Logisim project Projeto de circuito do Exemplo0076.circ as structural Verilog: 2 circuits, main circuit Exemplo0076
// 1x16
module \Memória_RAM_1x16  (
  input  CLK,
  input  ADDR,
  input  R_W,
  input  IN,
  input  CLR,
  output [15:0] OUT
);

  \Memória_RAM_1x8  \memória_ram_1x8_1  (.CLK(CLK), .ADDR(ADDR), .R_W(R_W), .IN(IN), .CLR(CLR), .OUT(OUT[7:0]));
  \Memória_RAM_1x8  \memória_ram_1x8_2  (.CLK(CLK), .ADDR(ADDR), .R_W(R_W), .IN(IN), .CLR(CLR), .OUT(OUT[15:8]));

  // Notes on the sheet:
  //   Matrícula: 448662
  //   Nome: Josemar Alves Caetano
endmodule

module Exemplo0076 (
  input  ADDR,
  input  R_W,
  input  IN,
  input  CLR,
  output [15:0] OUT
);

  wire clock_1_out;

  Clock clock_1 (.out(clock_1_out));
  \Memória_RAM_1x16  \memória_ram_1x16_1  (.CLK(clock_1_out), .ADDR(ADDR), .R_W(R_W), .IN(IN), .CLR(CLR), .OUT(OUT));

  // Notes on the sheet:
  //   Matrícula: 448662
  //   Nome: Josemar Alves Caetano
endmodule
