// Logisim project Projeto de circuito do Exemplo0077.circ as structural Verilog: 2 circuits, main circuit Exemplo0077
// 4x8
module \Memória_RAM_4x8  (
  input  CLK,
  input  [3:0] ADDR,
  input  R_W,
  input  IN,
  input  CLR,
  output [31:0] OUT
);

  \Memória_RAM_1x8  \memória_ram_1x8_1  (.CLK(CLK), .ADDR(ADDR[0]), .R_W(R_W), .IN(IN), .CLR(CLR), .OUT(OUT[7:0]));
  \Memória_RAM_1x8  \memória_ram_1x8_2  (.CLK(CLK), .ADDR(ADDR[1]), .R_W(R_W), .IN(IN), .CLR(CLR), .OUT(OUT[15:8]));
  \Memória_RAM_1x8  \memória_ram_1x8_3  (.CLK(CLK), .ADDR(ADDR[2]), .R_W(R_W), .IN(IN), .CLR(CLR), .OUT(OUT[23:16]));
  \Memória_RAM_1x8  \memória_ram_1x8_4  (.CLK(CLK), .ADDR(ADDR[3]), .R_W(R_W), .IN(IN), .CLR(CLR), .OUT(OUT[31:24]));

  // Notes on the sheet:
  //   Matrícula: 448662
  //   Nome: Josemar Alves Caetano
endmodule

module Exemplo0077 (
  input  [3:0] ADDR,
  input  R_W,
  input  IN,
  input  CLR,
  output [31:0] OUT
);

  wire clock_1_out;

  Clock clock_1 (.out(clock_1_out));
  \Memória_RAM_4x8  \memória_ram_4x8_1  (.CLK(clock_1_out), .ADDR(ADDR), .R_W(R_W), .IN(IN), .CLR(CLR), .OUT(OUT));

  // Notes on the sheet:
  //   Matrícula: 448662
  //   Nome: Josemar Alves Caetano
endmodule
