// Logisim project logisimteste.circ as structural Verilog
// 1X4
module RAM_1X4 (
  input  clock,
  input  r_w,
  input  addr,
  input  clr,
  input  [3:0] \input ,
  output [3:0] \output 
);

  wire and_1_out, j_k_ff_1_q, j_k_ff_2_q, j_k_ff_3_q, j_k_ff_4_q, not_1_out, not_2_out, not_3_out, not_4_out,
       not_5_out;
  wire [3:0] and_5_out;

  not not_1 (not_1_out, r_w);
  and and_1 (and_1_out, clock, r_w, addr);
  not not_2 (not_2_out, \input [3]);
  and and_2 (and_5_out[3], addr, j_k_ff_1_q);
  J_K_Flip_Flop j_k_ff_1 (
    .J(\input [3]), .clk(and_1_out), .K(not_2_out), .Q(j_k_ff_1_q), .reset(clr));  // open: Qn, preset, en
  not not_3 (not_3_out, \input [2]);
  and and_3 (and_5_out[2], addr, j_k_ff_2_q);
  J_K_Flip_Flop j_k_ff_2 (
    .J(\input [2]), .clk(and_1_out), .K(not_3_out), .Q(j_k_ff_2_q), .reset(clr));  // open: Qn, preset, en
  assign \output  = not_1_out ? and_5_out : 4'bz;  // Controlled_Buffer controlled_buffer_1
  not not_4 (not_4_out, \input [1]);
  and and_4 (and_5_out[1], addr, j_k_ff_3_q);
  J_K_Flip_Flop j_k_ff_3 (
    .J(\input [1]), .clk(and_1_out), .K(not_4_out), .Q(j_k_ff_3_q), .reset(clr));  // open: Qn, preset, en
  and and_5 (and_5_out[0], addr, j_k_ff_4_q);
  J_K_Flip_Flop j_k_ff_4 (
    .J(\input [0]), .clk(and_1_out), .K(not_5_out), .Q(j_k_ff_4_q), .reset(clr));  // open: Qn, preset, en
  not not_5 (not_5_out, \input [0]);

  // Notes on the sheet:
  //   Exercicio001 - Átila Martins Silva Júnior - 449014
  //   r/w:
  //   1-ler entrada
  //   0-mostra
endmodule

// 2X4
module RAM_2X4 (
  input  [3:0] \input ,
  input  clk,
  input  r_w,
  input  addr,
  input  clr,
  output [3:0] \output 
);

  wire demultiplexer_1_out0, demultiplexer_1_out1;
  wire [3:0] ram_1x4_1_output, ram_1x4_2_output;

  Demultiplexer #(.enable("false")) demultiplexer_1 (
    .out0(demultiplexer_1_out0), .out1(demultiplexer_1_out1), .in(1'b1), .sel(addr));
  RAM_1X4 ram_1x4_1 (
    .clock(clk), .r_w(r_w), .addr(demultiplexer_1_out0), .\output (ram_1x4_1_output), .\input (\input ),
    .clr(clr));
  RAM_1X4 ram_1x4_2 (
    .clock(clk), .r_w(r_w), .addr(demultiplexer_1_out1), .\output (ram_1x4_2_output), .\input (\input ),
    .clr(clr));
  Multiplexer #(.width(4), .enable("false")) multiplexer_1 (
    .in0(ram_1x4_1_output), .in1(ram_1x4_2_output), .out(\output ), .sel(addr));

  // Notes on the sheet:
  //   Exercicio002 - Átila Martins Silva Júnior - 449014
  //   r/w:
  //   1-ler entrada
  //   0-mostra
endmodule

// 1X8
module RAM_1X8 (
  input  [7:0] \input ,
  input  clk,
  input  r_w,
  input  addr_1,
  input  clr,
  output [7:0] \output 
);

  RAM_1X4 ram_1x4_1 (
    .clock(clk), .r_w(r_w), .addr(addr_1), .\output (\output [7:4]), .\input (\input [7:4]), .clr(clr));
  RAM_1X4 ram_1x4_2 (
    .clock(clk), .r_w(r_w), .addr(addr_1), .\output (\output [3:0]), .\input (\input [3:0]), .clr(clr));

  // Notes on the sheet:
  //   Exercicio003 - Átila Martins Silva Júnior - 449014
  //   r/w:
  //   1-ler entrada
  //   0-mostra
endmodule

// 4x8
module RAM_4X8_0 (
  input  [7:0] in_1,
  input  clk,
  input  r_w,
  input  [1:0] addr,
  input  clr,
  output [7:0] out_6
);

  wire demultiplexer_1_out0, demultiplexer_1_out1, demultiplexer_1_out2, demultiplexer_1_out3;
  wire [3:0] ram_1x4_1_output, ram_1x4_2_output, ram_1x4_3_output, ram_1x4_4_output;
  wire [7:0] ram_1x4_7_output, ram_1x4_8_output;

  Demultiplexer #(.select(2), .enable("false")) demultiplexer_1 (
    .out0(demultiplexer_1_out0), .out1(demultiplexer_1_out1), .out2(demultiplexer_1_out2),
    .out3(demultiplexer_1_out3), .in(1'b1), .sel(addr));
  RAM_1X4 ram_1x4_1 (
    .clock(clk), .r_w(r_w), .addr(demultiplexer_1_out0), .\output (ram_1x4_1_output), .\input (in_1[7:4]),
    .clr(clr));
  RAM_1X4 ram_1x4_2 (
    .clock(clk), .r_w(r_w), .addr(demultiplexer_1_out2), .\output (ram_1x4_2_output), .\input (in_1[7:4]),
    .clr(clr));
  RAM_1X4 ram_1x4_3 (
    .clock(clk), .r_w(r_w), .addr(demultiplexer_1_out0), .\output (ram_1x4_3_output), .\input (in_1[3:0]),
    .clr(clr));
  RAM_1X4 ram_1x4_4 (
    .clock(clk), .r_w(r_w), .addr(demultiplexer_1_out2), .\output (ram_1x4_4_output), .\input (in_1[3:0]),
    .clr(clr));
  Multiplexer #(.select(2), .width(8), .enable("false")) multiplexer_1 (
    .in0({ram_1x4_1_output, ram_1x4_3_output}), .in1(ram_1x4_7_output),
    .in2({ram_1x4_2_output, ram_1x4_4_output}), .in3(ram_1x4_8_output), .out(out_6), .sel(addr));
  RAM_1X4 ram_1x4_5 (
    .clock(clk), .r_w(r_w), .addr(demultiplexer_1_out1), .\output (ram_1x4_7_output[7:4]),
    .\input (in_1[7:4]), .clr(clr));
  RAM_1X4 ram_1x4_6 (
    .clock(clk), .r_w(r_w), .addr(demultiplexer_1_out3), .\output (ram_1x4_8_output[7:4]),
    .\input (in_1[7:4]), .clr(clr));
  RAM_1X4 ram_1x4_7 (
    .clock(clk), .r_w(r_w), .addr(demultiplexer_1_out1), .\output (ram_1x4_7_output[3:0]),
    .\input (in_1[3:0]), .clr(clr));
  RAM_1X4 ram_1x4_8 (
    .clock(clk), .r_w(r_w), .addr(demultiplexer_1_out3), .\output (ram_1x4_8_output[3:0]),
    .\input (in_1[3:0]), .clr(clr));

  // Notes on the sheet:
  //   r/w:
  //   1-ler entrada
  //   0-mostra
  //   Exercicio004 - Átila Martins Silva Júnior - 449014
endmodule

module RAM_8X8 (
  input  [7:0] \input ,
  input  clk,
  input  r_w,
  input  [2:0] addr,
  input  clr,
  output [7:0] \output 
);

  wire demultiplexer_1_out0, demultiplexer_1_out1;
  wire [7:0] ram_4x8_1_1_output, ram_4x8_1_2_output;

  Demultiplexer #(.enable("false")) demultiplexer_1 (
    .out0(demultiplexer_1_out0), .out1(demultiplexer_1_out1), .in(clk), .sel(addr[2]));
  RAM_4X8_1 ram_4x8_1_1 (
    .clk(demultiplexer_1_out0), .r_w(r_w), .addr(addr[1:0]), .clr(clr), .\input (\input ),
    .\output (ram_4x8_1_1_output));
  Multiplexer #(.width(8), .enable("false")) multiplexer_1 (
    .in0(ram_4x8_1_1_output), .in1(ram_4x8_1_2_output), .out(\output ), .sel(addr[2]));
  RAM_4X8_1 ram_4x8_1_2 (
    .clk(demultiplexer_1_out1), .r_w(r_w), .addr(addr[1:0]), .clr(clr), .\input (\input ),
    .\output (ram_4x8_1_2_output));

  // Notes on the sheet:
  //   Exercicio005 - Átila Martins Silva Júnior - 449014
  //   r/w:
  //   1-ler entrada
  //   0-mostra
endmodule

// 1X16
module RAM_1X16 (
  input  [15:0] in_1,
  input  clk,
  input  r_w,
  input  addr_1,
  input  clr,
  output [15:0] out_6
);

  RAM_1X8 ram_1x8_1 (.clk(clk), .r_w(r_w), .addr_1(addr_1), .clr(clr), .\input (in_1[15:8]), .\output (out_6[15:8]));
  RAM_1X8 ram_1x8_2 (.clk(clk), .r_w(r_w), .addr_1(addr_1), .clr(clr), .\input (in_1[7:0]), .\output (out_6[7:0]));

  // Notes on the sheet:
  //   Exercicio006 - Átila Martins Silva Júnior - 449014
  //   r/w:
  //   1-ler entrada
  //   0-mostra
  //   input
  //   output
endmodule

// 4X8
module RAM_4X8_1 (
  input  [7:0] \input ,
  input  clk,
  input  r_w,
  input  [1:0] addr,
  input  clr,
  output [7:0] \output 
);

  wire demultiplexer_1_out0, demultiplexer_1_out1, demultiplexer_1_out2, demultiplexer_1_out3;
  wire [7:0] ram_1x8_1_output, ram_1x8_2_output, ram_1x8_3_output, ram_1x8_4_output;

  Demultiplexer #(.select(2), .enable("false")) demultiplexer_1 (
    .out0(demultiplexer_1_out0), .out1(demultiplexer_1_out1), .out2(demultiplexer_1_out2),
    .out3(demultiplexer_1_out3), .in(1'b1), .sel(addr));
  RAM_1X8 ram_1x8_1 (
    .clk(clk), .r_w(r_w), .addr_1(demultiplexer_1_out0), .clr(clr), .\input (\input ),
    .\output (ram_1x8_1_output));
  RAM_1X8 ram_1x8_2 (
    .clk(clk), .r_w(r_w), .addr_1(demultiplexer_1_out2), .clr(clr), .\input (\input ),
    .\output (ram_1x8_2_output));
  Multiplexer #(.select(2), .width(8), .enable("false")) multiplexer_1 (
    .in0(ram_1x8_1_output), .in1(ram_1x8_3_output), .in2(ram_1x8_2_output), .in3(ram_1x8_4_output),
    .out(\output ), .sel(addr));
  RAM_1X8 ram_1x8_3 (
    .clk(clk), .r_w(r_w), .addr_1(demultiplexer_1_out1), .clr(clr), .\input (\input ),
    .\output (ram_1x8_3_output));
  RAM_1X8 ram_1x8_4 (
    .clk(clk), .r_w(r_w), .addr_1(demultiplexer_1_out3), .clr(clr), .\input (\input ),
    .\output (ram_1x8_4_output));

  // Notes on the sheet:
  //   Exercicio007 - Átila Martins Silva Júnior - 449014
  //   r/w:
  //   1-ler entrada
  //   0-mostra
endmodule
