// Logisim project circuito.circ as structural Verilog: 6 circuits, main circuit main
module main (
  input  in_1,
  input  [3:0] in_2,
  input  in_3,
  input  in_4,
  input  in_5,
  output [3:0] out_6
);

  wire demultiplexer_1_out0, demultiplexer_1_out1;
  wire [3:0] ram1x4_1_out_6, ram1x4_2_out_6;

  Demultiplexer #(.enable("false")) demultiplexer_1 (
    .out0(demultiplexer_1_out0), .out1(demultiplexer_1_out1), .in(1'b1), .sel(in_1));
  ram1X4 ram1x4_1 (
    .in_2(demultiplexer_1_out0), .in_3(in_3), .in_4(in_4), .in_5(in_5), .in_1(in_2), .out_6(ram1x4_1_out_6));
  ram1X4 ram1x4_2 (
    .in_2(demultiplexer_1_out1), .in_3(in_3), .in_4(in_4), .in_5(in_5), .in_1(in_2), .out_6(ram1x4_2_out_6));
  Multiplexer #(.width(4), .enable("false")) multiplexer_1 (
    .in0(ram1x4_1_out_6), .in1(ram1x4_2_out_6), .out(out_6), .sel(in_1));
endmodule

// RAM 1X4
module ram1X4 (
  input  [3:0] in_1,
  input  in_2,
  input  in_3,
  input  in_4,
  input  in_5,
  output [3:0] out_6
);

  wire and_1_out, not_1_out, not_2_out, not_3_out, not_4_out;

  and and_1 (and_1_out, in_2, in_3, in_4);
  not not_1 (not_1_out, in_1[3]);
  J_K_Flip_Flop j_k_ff_1 (
    .J(in_1[3]), .clk(and_1_out), .K(not_1_out), .Q(out_6[3]), .reset(in_5));  // open: Qn, preset, en
  not not_2 (not_2_out, in_1[2]);
  J_K_Flip_Flop j_k_ff_2 (
    .J(in_1[2]), .clk(and_1_out), .K(not_2_out), .Q(out_6[2]), .reset(in_5));  // open: Qn, preset, en
  J_K_Flip_Flop j_k_ff_3 (
    .J(in_1[1]), .clk(and_1_out), .K(not_3_out), .Q(out_6[1]), .reset(in_5));  // open: Qn, preset, en
  not not_3 (not_3_out, in_1[1]);
  J_K_Flip_Flop j_k_ff_4 (
    .J(in_1[0]), .clk(and_1_out), .K(not_4_out), .Q(out_6[0]), .reset(in_5));  // open: Qn, preset, en
  not not_4 (not_4_out, in_1[0]);

  // Notes on the sheet:
  //   Guilherme Alves de OLiveira
endmodule

module exercicio2 (
  input  in_1,
  input  [3:0] in_2,
  input  in_3,
  input  in_4,
  input  in_5,
  output [3:0] out_6
);

  wire demultiplexer_1_out0, demultiplexer_1_out1;
  wire [3:0] ram1x4_1_out_6, ram1x4_2_out_6;

  Demultiplexer #(.enable("false")) demultiplexer_1 (
    .out0(demultiplexer_1_out0), .out1(demultiplexer_1_out1), .in(1'b1), .sel(in_1));
  ram1X4 ram1x4_1 (
    .in_2(demultiplexer_1_out0), .in_3(in_3), .in_4(in_4), .in_5(in_5), .in_1(in_2), .out_6(ram1x4_1_out_6));
  ram1X4 ram1x4_2 (
    .in_2(demultiplexer_1_out1), .in_3(in_3), .in_4(in_4), .in_5(in_5), .in_1(in_2), .out_6(ram1x4_2_out_6));
  Multiplexer #(.width(4), .enable("false")) multiplexer_1 (
    .in0(ram1x4_1_out_6), .in1(ram1x4_2_out_6), .out(out_6), .sel(in_1));
endmodule

module exericio3 (
  input  in_1,
  input  [3:0] in_2,
  input  [3:0] in_3,
  input  in_4,
  input  in_5,
  input  in_6,
  output [3:0] out_7,
  output [3:0] out_8
);

  ram1X4 ram1x4_1 (.in_2(in_1), .in_3(in_4), .in_4(in_5), .in_5(in_6), .in_1(in_2), .out_6(out_7));
  ram1X4 ram1x4_2 (.in_2(in_1), .in_3(in_4), .in_4(in_5), .in_5(in_6), .in_1(in_3), .out_6(out_8));
endmodule

module exercicio4 (
  input  [1:0] in_1,
  input  [7:0] in_2,
  input  in_3,
  input  in_4,
  input  in_5,
  output [7:0] out_6
);

  wire demultiplexer_1_out0, demultiplexer_1_out1, demultiplexer_1_out2, demultiplexer_1_out3;
  wire [3:0] ram1x4_1_out_6, ram1x4_2_out_6, ram1x4_3_out_6, ram1x4_4_out_6, ram1x4_5_out_6, ram1x4_6_out_6,
       ram1x4_7_out_6, ram1x4_8_out_6;

  Demultiplexer #(.select(2), .enable("false")) demultiplexer_1 (
    .out0(demultiplexer_1_out0), .out1(demultiplexer_1_out1), .out2(demultiplexer_1_out2),
    .out3(demultiplexer_1_out3), .in(1'b1), .sel(in_1));
  ram1X4 ram1x4_1 (
    .in_2(demultiplexer_1_out0), .in_3(in_3), .in_4(in_4), .in_5(in_5), .in_1(in_2[3:0]),
    .out_6(ram1x4_1_out_6));
  ram1X4 ram1x4_2 (
    .in_2(demultiplexer_1_out0), .in_3(in_3), .in_4(in_4), .in_5(in_5), .in_1(in_2[7:4]),
    .out_6(ram1x4_2_out_6));
  ram1X4 ram1x4_3 (
    .in_2(demultiplexer_1_out1), .in_3(in_3), .in_4(in_4), .in_5(in_5), .in_1(in_2[3:0]),
    .out_6(ram1x4_3_out_6));
  ram1X4 ram1x4_4 (
    .in_2(demultiplexer_1_out1), .in_3(in_3), .in_4(in_4), .in_5(in_5), .in_1(in_2[7:4]),
    .out_6(ram1x4_4_out_6));
  ram1X4 ram1x4_5 (
    .in_2(demultiplexer_1_out2), .in_3(in_3), .in_4(in_4), .in_5(in_5), .in_1(in_2[3:0]),
    .out_6(ram1x4_5_out_6));
  ram1X4 ram1x4_6 (
    .in_2(demultiplexer_1_out2), .in_3(in_3), .in_4(in_4), .in_5(in_5), .in_1(in_2[7:4]),
    .out_6(ram1x4_6_out_6));
  ram1X4 ram1x4_7 (
    .in_2(demultiplexer_1_out3), .in_3(in_3), .in_4(in_4), .in_5(in_5), .in_1(in_2[3:0]),
    .out_6(ram1x4_7_out_6));
  ram1X4 ram1x4_8 (
    .in_2(demultiplexer_1_out3), .in_3(in_3), .in_4(in_4), .in_5(in_5), .in_1(in_2[7:4]),
    .out_6(ram1x4_8_out_6));
  Multiplexer #(.select(2), .width(8), .enable("false")) multiplexer_1 (
    .in0({ram1x4_2_out_6, ram1x4_1_out_6}), .in1({ram1x4_4_out_6, ram1x4_3_out_6}),
    .in2({ram1x4_6_out_6, ram1x4_5_out_6}), .in3({ram1x4_8_out_6, ram1x4_7_out_6}), .out(out_6), .sel(in_1));
endmodule

module demux (
  input  [7:0] in_1,
  input  in_2,
  input  in_3,
  input  in_4,
  input  in_5,
  output [1:0] out_6,
  output [7:0] out_7
);

  wire demultiplexer_1_out0, demultiplexer_1_out1, demultiplexer_2_out0, demultiplexer_2_out1,
       demultiplexer_3_out0, demultiplexer_3_out1, demultiplexer_4_out0, demultiplexer_4_out1,
       demultiplexer_5_out0, demultiplexer_5_out1, not_1_out;
  wire [1:0] or_3_out;
  wire [7:0] exercicio4_1_out_6, exercicio4_2_out_6;

  Demultiplexer #(.enable("false")) demultiplexer_1 (
    .out0(demultiplexer_1_out0), .out1(demultiplexer_1_out1), .in(1'b1), .sel(in_2));
  Demultiplexer #(.enable("false")) demultiplexer_2 (
    .out0(demultiplexer_2_out0), .out1(demultiplexer_2_out1), .in(in_4), .sel(demultiplexer_1_out0));
  Demultiplexer #(.enable("false")) demultiplexer_3 (
    .out0(demultiplexer_3_out0), .out1(demultiplexer_3_out1), .in(in_3), .sel(in_3));
  Demultiplexer #(.enable("false")) demultiplexer_4 (
    .out0(demultiplexer_4_out0), .out1(demultiplexer_4_out1), .in(in_4), .sel(demultiplexer_1_out1));
  Demultiplexer #(.enable("false")) demultiplexer_5 (
    .out0(demultiplexer_5_out0), .out1(demultiplexer_5_out1), .in(in_3), .sel(in_3));
  or or_1 (out_6[0], demultiplexer_3_out1, demultiplexer_2_out0);
  or or_2 (out_6[1], demultiplexer_2_out1, demultiplexer_3_out0);
  or or_3 (or_3_out[0], demultiplexer_5_out1, demultiplexer_4_out0);
  or or_4 (or_3_out[1], demultiplexer_4_out1, demultiplexer_5_out0);
  not not_1 (not_1_out, in_2);
  exercicio4 exercicio4_1 (
    .in_1(out_6), .in_3(in_5), .in_4(not_1_out), .in_2(in_1), .out_6(exercicio4_1_out_6));  // open: in_5
  exercicio4 exercicio4_2 (
    .in_1(or_3_out), .in_3(in_5), .in_4(in_2), .in_2(in_1), .out_6(exercicio4_2_out_6));  // open: in_5
  Multiplexer #(.width(8), .enable("false")) multiplexer_1 (
    .in0(exercicio4_1_out_6), .in1(exercicio4_2_out_6), .out(out_7), .sel(in_2));
endmodule
