// Logisim project Circuitos.circ as structural Verilog: 9 circuits, main circuit main
module main (
);


  // Notes on the sheet:
  //   Guia 10
  //   Isabel Bicalho Amaro
  //   Matricula: 451580
endmodule

// 1x1
module Questao1 (
  input  Addr,
  input  RW,
  input  clk,
  input  in,
  input  clr,
  output out
);

  wire and_1_out, j_k_ff_1_q, not_1_out;

  and and_1 (and_1_out, Addr, RW, clk);
  not not_1 (not_1_out, in);
  and and_2 (out, Addr, j_k_ff_1_q);
  J_K_Flip_Flop j_k_ff_1 (.J(in), .clk(and_1_out), .K(not_1_out), .Q(j_k_ff_1_q), .reset(clr));  // open: Qn, preset, en

  // Notes on the sheet:
  //   Guia 10
  //   Isabel Bicalho Amaro
  //   Matricula: 451580
endmodule

// 1x4
module Questao1a (
  input  Addr,
  input  R_W,
  input  clk,
  input  [3:0] in,
  input  clr,
  output [3:0] out
);

  Questao1 questao1_1 (.Addr(Addr), .RW(R_W), .clk(clk), .in(in[0]), .clr(clr), .out(out[0]));
  Questao1 questao1_2 (.Addr(Addr), .RW(R_W), .clk(clk), .in(in[1]), .clr(clr), .out(out[1]));
  Questao1 questao1_3 (.Addr(Addr), .RW(R_W), .clk(clk), .in(in[2]), .clr(clr), .out(out[2]));
  Questao1 questao1_4 (.Addr(Addr), .RW(R_W), .clk(clk), .in(in[3]), .clr(clr), .out(out[3]));

  // Notes on the sheet:
  //   Guia 10
  //   Matricula: 451580
  //   Isabel Bicalho Amaro
endmodule

// 2x4
module Questao2 (
  input  Addr,
  input  R_W,
  input  clk,
  input  [3:0] in,
  input  clr,
  output [3:0] out
);

  wire demultiplexer_1_out0, demultiplexer_1_out1;
  wire [3:0] questao1a_1_out, questao1a_2_out;

  Demultiplexer demultiplexer_1 (
    .out0(demultiplexer_1_out0), .out1(demultiplexer_1_out1), .in(1'b1), .sel(Addr));  // open: en
  Questao1a questao1a_1 (.Addr(demultiplexer_1_out0), .R_W(R_W), .clk(clk), .in(in), .clr(clr), .out(questao1a_1_out));
  Questao1a questao1a_2 (.Addr(demultiplexer_1_out1), .R_W(R_W), .clk(clk), .in(in), .clr(clr), .out(questao1a_2_out));
  Multiplexer #(.width(4)) multiplexer_1 (
    .in0(questao1a_1_out), .in1(questao1a_2_out), .out(out), .sel(Addr));  // open: en

  // Notes on the sheet:
  //   Guia 10
  //   Matricula: 451580
  //   Isabel Bicalho Amaro
endmodule

// 1x8
module Questao3 (
  input  Addr,
  input  R_W,
  input  clk,
  input  [7:0] in,
  input  clr,
  output [7:0] out
);

  Questao1a questao1a_1 (.Addr(Addr), .R_W(R_W), .clk(clk), .in(in[3:0]), .clr(clr), .out(out[3:0]));
  Questao1a questao1a_2 (.Addr(Addr), .R_W(R_W), .clk(clk), .in(in[7:4]), .clr(clr), .out(out[7:4]));

  // Notes on the sheet:
  //   Guia 10
  //   Isabel Bicalho Amaro
  //   Matricula: 451580
endmodule

// 2x8
module Questao4 (
  input  Addr,
  input  R_W,
  input  clk,
  input  [7:0] in,
  input  clr,
  output [7:0] out
);

  wire demultiplexer_1_out0, demultiplexer_1_out1;
  wire [3:0] questao2_1_out, questao2_2_out, questao2_3_out, questao2_4_out;

  Demultiplexer demultiplexer_1 (
    .out0(demultiplexer_1_out0), .out1(demultiplexer_1_out1), .in(1'b1), .sel(Addr));  // open: en
  Questao2 questao2_1 (
    .Addr(demultiplexer_1_out0), .R_W(R_W), .clk(clk), .in(in[3:0]), .clr(clr), .out(questao2_1_out));
  Questao2 questao2_2 (
    .Addr(demultiplexer_1_out0), .R_W(R_W), .clk(clk), .in(in[7:4]), .clr(clr), .out(questao2_2_out));
  Questao2 questao2_3 (
    .Addr(demultiplexer_1_out1), .R_W(R_W), .clk(clk), .in(in[3:0]), .clr(clr), .out(questao2_3_out));
  Questao2 questao2_4 (
    .Addr(demultiplexer_1_out1), .R_W(R_W), .clk(clk), .in(in[7:4]), .clr(clr), .out(questao2_4_out));
  Multiplexer #(.width(8)) multiplexer_1 (
    .in0({questao2_2_out, questao2_1_out}), .in1({questao2_4_out, questao2_3_out}), .out(out), .sel(Addr));  // open: en

  // Notes on the sheet:
  //   Guia 10
  //   Isabel Bicalho Amaro
  //   Matricula: 451580
endmodule

module Questao5 (
  input  [2:0] Addr,
  input  R_W,
  input  clk,
  input  [7:0] in,
  input  clr,
  output [7:0] out
);

  wire demultiplexer_1_out0, demultiplexer_1_out1, demultiplexer_1_out2, demultiplexer_1_out3,
       demultiplexer_1_out4, demultiplexer_1_out5, demultiplexer_1_out6, demultiplexer_1_out7;
  wire [7:0] questao4_1_out, questao4_2_out, questao4_3_out, questao4_4_out, questao4_5_out, questao4_6_out,
       questao4_7_out, questao4_8_out;

  Demultiplexer #(.select(3)) demultiplexer_1 (
    .out0(demultiplexer_1_out0), .out1(demultiplexer_1_out1), .out2(demultiplexer_1_out2),
    .out3(demultiplexer_1_out3), .out4(demultiplexer_1_out4), .out5(demultiplexer_1_out5),
    .out6(demultiplexer_1_out6), .out7(demultiplexer_1_out7), .in(1'b1), .sel(Addr));  // open: en
  Questao4 questao4_1 (.Addr(demultiplexer_1_out0), .R_W(R_W), .clk(clk), .in(in), .clr(clr), .out(questao4_1_out));
  Questao4 questao4_2 (.Addr(demultiplexer_1_out1), .R_W(R_W), .clk(clk), .in(in), .clr(clr), .out(questao4_2_out));
  Questao4 questao4_3 (.Addr(demultiplexer_1_out2), .R_W(R_W), .clk(clk), .in(in), .clr(clr), .out(questao4_3_out));
  Questao4 questao4_4 (.Addr(demultiplexer_1_out3), .R_W(R_W), .clk(clk), .in(in), .clr(clr), .out(questao4_4_out));
  Questao4 questao4_5 (.Addr(demultiplexer_1_out4), .R_W(R_W), .clk(clk), .in(in), .clr(clr), .out(questao4_5_out));
  Questao4 questao4_6 (.Addr(demultiplexer_1_out5), .R_W(R_W), .clk(clk), .in(in), .clr(clr), .out(questao4_6_out));
  Questao4 questao4_7 (.Addr(demultiplexer_1_out6), .R_W(R_W), .clk(clk), .in(in), .clr(clr), .out(questao4_7_out));
  Questao4 questao4_8 (.Addr(demultiplexer_1_out7), .R_W(R_W), .clk(clk), .in(in), .clr(clr), .out(questao4_8_out));
  Multiplexer #(.select(3), .width(8)) multiplexer_1 (
    .in0(questao4_1_out), .in1(questao4_2_out), .in2(questao4_3_out), .in3(questao4_4_out),
    .in4(questao4_5_out), .in5(questao4_6_out), .in6(questao4_7_out), .in7(questao4_8_out), .out(out),
    .sel(Addr));  // open: en

  // Notes on the sheet:
  //   Guia 10
  //   Isabel Bicalho Amaro
  //   Matricula: 451580
endmodule

module Questao6 (
  input  Addr,
  input  R_W,
  input  clk,
  input  [15:0] in,
  input  clr,
  output [15:0] out
);

  Questao3 questao3_1 (.Addr(Addr), .R_W(R_W), .clk(clk), .in(in[7:0]), .clr(clr), .out(out[15:8]));
  Questao3 questao3_2 (.Addr(Addr), .R_W(R_W), .clk(clk), .in(in[15:8]), .clr(clr), .out(out[7:0]));

  // Notes on the sheet:
  //   Guia 10
  //   Isabel Bicalho Amaro
  //   Matricula: 451580
endmodule

module Questao7 (
  input  [1:0] Addr,
  input  R_W,
  input  clk,
  input  [7:0] in,
  input  clr,
  output [7:0] out
);

  wire demultiplexer_1_out0, demultiplexer_1_out1, demultiplexer_1_out2, demultiplexer_1_out3;
  wire [7:0] questao3_1_out, questao3_2_out, questao3_3_out, questao3_4_out;

  Demultiplexer #(.select(2)) demultiplexer_1 (
    .out0(demultiplexer_1_out0), .out1(demultiplexer_1_out1), .out2(demultiplexer_1_out2),
    .out3(demultiplexer_1_out3), .in(1'b1), .sel(Addr));  // open: en
  Questao3 questao3_1 (.Addr(demultiplexer_1_out0), .R_W(R_W), .clk(clk), .in(in), .clr(clr), .out(questao3_1_out));
  Questao3 questao3_2 (.Addr(demultiplexer_1_out1), .R_W(R_W), .clk(clk), .in(in), .clr(clr), .out(questao3_2_out));
  Questao3 questao3_3 (.Addr(demultiplexer_1_out2), .R_W(R_W), .clk(clk), .in(in), .clr(clr), .out(questao3_3_out));
  Questao3 questao3_4 (.Addr(demultiplexer_1_out3), .R_W(R_W), .clk(clk), .in(in), .clr(clr), .out(questao3_4_out));
  Multiplexer #(.select(2), .width(8)) multiplexer_1 (
    .in0(questao3_1_out), .in1(questao3_2_out), .in2(questao3_3_out), .in3(questao3_4_out), .out(out),
    .sel(Addr));  // open: en

  // Notes on the sheet:
  //   Guia 10
  //   Matricula: 451580
  //   Isabel Bicalho Amaro
endmodule
