// Logisim project exercicio02.circ as structural Verilog: 4 circuits, main circuit RAM 2x4
module main (
  input  in_1,
  input  in_2,
  input  in_3,
  input  in_4,
  input  in_5,
  output out_6
);

  wire and_1_out, j_k_ff_1_q, not_1_out;

  and and_1 (and_1_out, in_1, in_2, in_3);
  not not_1 (not_1_out, in_4);
  J_K_Flip_Flop j_k_ff_1 (
    .J(in_4), .clk(and_1_out), .K(not_1_out), .Q(j_k_ff_1_q), .reset(in_5));  // open: Qn, preset, en
  and and_2 (out_6, in_1, j_k_ff_1_q);
endmodule

module RAM (
  input  in_1,
  input  in_2,
  input  in_3,
  input  [1:0] in_4,
  input  in_5,
  output [1:0] out_6
);

  main main_1 (.in_1(in_1), .in_2(in_2), .in_3(in_3), .in_4(in_4[0]), .out_6(out_6[0]), .in_5(in_5));
  main main_2 (.in_1(in_1), .in_2(in_2), .in_3(in_3), .in_4(in_4[1]), .out_6(out_6[1]), .in_5(in_5));
endmodule

module RAM_1X4 (
  input  in_1,
  input  in_2,
  input  in_3,
  input  [3:0] in_4,
  input  in_5,
  output [3:0] out_6
);

  RAM ram_1 (.in_1(in_1), .in_2(in_2), .in_4(in_4[1:0]), .out_6(out_6[1:0]), .in_5(in_5), .in_3(in_3));
  RAM ram_2 (.in_1(in_1), .in_2(in_2), .in_4(in_4[3:2]), .out_6(out_6[3:2]), .in_5(in_5), .in_3(in_3));
endmodule

module RAM_2x4 (
  input  ADDR,
  input  R___W,
  input  [3:0] DATA,
  input  in_4,
  output [3:0] SAIDA
);

  wire clock_1_out, demultiplexer_1_out0, demultiplexer_1_out1;
  wire [3:0] ram_1x4_1_out_6, ram_1x4_2_out_6;

  Demultiplexer #(.enable("false")) demultiplexer_1 (
    .out0(demultiplexer_1_out0), .out1(demultiplexer_1_out1), .in(1'b1), .sel(ADDR));
  Clock clock_1 (.out(clock_1_out));
  RAM_1X4 ram_1x4_1 (
    .in_1(demultiplexer_1_out1), .in_2(R___W), .in_4(DATA), .out_6(ram_1x4_1_out_6), .in_5(in_4),
    .in_3(clock_1_out));
  RAM_1X4 ram_1x4_2 (
    .in_1(demultiplexer_1_out0), .in_2(R___W), .in_4(DATA), .out_6(ram_1x4_2_out_6), .in_5(in_4),
    .in_3(clock_1_out));
  Multiplexer #(.width(4), .enable("false")) multiplexer_1 (
    .in0(ram_1x4_2_out_6), .in1(ram_1x4_1_out_6), .out(SAIDA), .sel(ADDR));

  // Notes on the sheet:
  //   CLK
  //   Rodolfo Herman - 451612
endmodule
