// Logisim project exercicio05.circ as structural Verilog: 6 circuits, main circuit RAM 8x8
module main (
  input  in_1,
  input  in_2,
  input  in_3,
  input  in_4,
  input  in_5,
  output out_6
);

  wire and_1_out, d_ff_1_q;

  and and_1 (and_1_out, in_1, in_2, in_3);
  D_Flip_Flop d_ff_1 (.clk(and_1_out), .D(in_4), .Q(d_ff_1_q), .reset(in_5));  // open: Qn, preset, en
  and and_2 (out_6, in_1, d_ff_1_q);
endmodule

module RAM (
  input  in_1,
  input  in_2,
  input  in_3,
  input  [1:0] in_4,
  input  in_5,
  output [1:0] out_6
);

  main main_1 (.in_1(in_1), .in_2(in_2), .in_3(in_3), .in_4(in_4[0]), .out_6(out_6[0]), .in_5(in_5));
  main main_2 (.in_1(in_1), .in_2(in_2), .in_3(in_3), .in_4(in_4[1]), .out_6(out_6[1]), .in_5(in_5));
endmodule

module RAM_1X4 (
  input  in_1,
  input  in_2,
  input  in_3,
  input  [3:0] in_4,
  input  in_5,
  output [3:0] out_6
);

  RAM ram_1 (.in_1(in_1), .in_2(in_2), .in_4(in_4[1:0]), .out_6(out_6[1:0]), .in_5(in_5), .in_3(in_3));
  RAM ram_2 (.in_1(in_1), .in_2(in_2), .in_4(in_4[3:2]), .out_6(out_6[3:2]), .in_5(in_5), .in_3(in_3));
endmodule

module RAM_4x8 (
  input  [1:0] in_1,
  input  in_2,
  input  in_3,
  input  [7:0] in_4,
  input  in_5,
  output [7:0] out_6
);

  wire demultiplexer_1_out0, demultiplexer_1_out1, demultiplexer_1_out2, demultiplexer_1_out3;
  wire [3:0] ram_1x4_1_out_6, ram_1x4_2_out_6, ram_1x4_3_out_6, ram_1x4_4_out_6, ram_1x4_7_out_6,
       ram_1x4_8_out_6;
  wire [7:0] ram_1x4_5_out_6;

  Demultiplexer #(.select(2), .enable("false")) demultiplexer_1 (
    .out0(demultiplexer_1_out0), .out1(demultiplexer_1_out1), .out2(demultiplexer_1_out2),
    .out3(demultiplexer_1_out3), .in(1'b1), .sel(in_1));
  RAM_1X4 ram_1x4_1 (
    .in_1(demultiplexer_1_out0), .in_2(in_2), .in_4(in_4[3:0]), .out_6(ram_1x4_1_out_6), .in_5(in_5),
    .in_3(in_3));
  RAM_1X4 ram_1x4_2 (
    .in_1(demultiplexer_1_out0), .in_2(in_2), .in_4(in_4[7:4]), .out_6(ram_1x4_2_out_6), .in_5(in_5),
    .in_3(in_3));
  RAM_1X4 ram_1x4_3 (
    .in_1(demultiplexer_1_out1), .in_2(in_2), .in_4(in_4[3:0]), .out_6(ram_1x4_3_out_6), .in_5(in_5),
    .in_3(in_3));
  RAM_1X4 ram_1x4_4 (
    .in_1(demultiplexer_1_out1), .in_2(in_2), .in_4(in_4[7:4]), .out_6(ram_1x4_4_out_6), .in_5(in_5),
    .in_3(in_3));
  RAM_1X4 ram_1x4_5 (
    .in_1(demultiplexer_1_out2), .in_2(in_2), .in_4(in_4[3:0]), .out_6(ram_1x4_5_out_6[3:0]), .in_5(in_5),
    .in_3(in_3));
  RAM_1X4 ram_1x4_6 (
    .in_1(demultiplexer_1_out2), .in_2(in_2), .in_4(in_4[7:4]), .out_6(ram_1x4_5_out_6[7:4]), .in_5(in_5),
    .in_3(in_3));
  RAM_1X4 ram_1x4_7 (
    .in_1(demultiplexer_1_out3), .in_2(in_2), .in_4(in_4[3:0]), .out_6(ram_1x4_7_out_6), .in_5(in_5),
    .in_3(in_3));
  RAM_1X4 ram_1x4_8 (
    .in_1(demultiplexer_1_out3), .in_2(in_2), .in_4(in_4[7:4]), .out_6(ram_1x4_8_out_6), .in_5(in_5),
    .in_3(in_3));
  Multiplexer #(.select(2), .width(8), .enable("false")) multiplexer_1 (
    .in0({ram_1x4_2_out_6, ram_1x4_1_out_6}), .in1({ram_1x4_4_out_6, ram_1x4_3_out_6}),
    .in2(ram_1x4_5_out_6), .in3({ram_1x4_8_out_6, ram_1x4_7_out_6}), .out(out_6), .sel(in_1));
endmodule

module RAM_8x8 (
  input  in_1,
  input  in_2,
  input  [7:0] in_3,
  input  in_4,
  output [7:0] out_5
);

  wire clock_1_out;
  wire [1:1] demultiplexer_1_out0, demultiplexer_1_out1;
  wire [7:0] ram_4x8_1_out_6, ram_4x8_2_out_6;

  Clock clock_1 (.out(clock_1_out));
  Demultiplexer #(.enable("false")) demultiplexer_1 (
    .out0(demultiplexer_1_out0[1]), .out1(demultiplexer_1_out1[1]), .in(1'b1), .sel(in_1));
  RAM_4x8 ram_4x8_1 (
    .in_1({2{demultiplexer_1_out1[1]}}), .in_2(in_2), .in_5(in_4), .out_6(ram_4x8_1_out_6), .in_4(in_3),
    .in_3(clock_1_out));
  RAM_4x8 ram_4x8_2 (
    .in_1({2{demultiplexer_1_out0[1]}}), .in_2(in_2), .in_5(in_4), .out_6(ram_4x8_2_out_6), .in_4(in_3),
    .in_3(clock_1_out));
  Multiplexer #(.width(8), .enable("false")) multiplexer_1 (
    .in0(ram_4x8_2_out_6), .in1(ram_4x8_1_out_6), .out(out_5), .sel(in_1));

  // Notes on the sheet:
  //   Rodolfo Herman - 451612
endmodule

module RAM8x8 (
  input  [2:0] in_1
);

  RAM_4x8 ram_4x8_1 ();  // open: in_1, in_2, in_5, out_6, in_4, in_3
  RAM_4x8 ram_4x8_2 ();  // open: in_1, in_2, in_5, out_6, in_4, in_3
  RAM_4x8 ram_4x8_3 ();  // open: in_1, in_2, in_5, out_6, in_4, in_3
  RAM_4x8 ram_4x8_4 ();  // open: in_1, in_2, in_5, out_6, in_4, in_3
endmodule
