// Logisim project extra01.circ as structural Verilog: 5 circuits, main circuit RAM 1x16
module main (
  input  in_1,
  input  in_2,
  input  in_3,
  input  in_4,
  input  in_5,
  output out_6
);

  wire and_1_out, j_k_ff_1_q, not_1_out;

  and and_1 (and_1_out, in_1, in_2, in_3);
  not not_1 (not_1_out, in_4);
  J_K_Flip_Flop j_k_ff_1 (
    .J(in_4), .clk(and_1_out), .K(not_1_out), .Q(j_k_ff_1_q), .reset(in_5));  // open: Qn, preset, en
  and and_2 (out_6, in_1, j_k_ff_1_q);
endmodule

module RAM_1x2 (
  input  in_1,
  input  in_2,
  input  in_3,
  input  [1:0] in_4,
  input  in_5,
  output [1:0] out_6
);

  main main_1 (.in_1(in_1), .in_2(in_2), .in_3(in_3), .in_4(in_4[0]), .out_6(out_6[0]), .in_5(in_5));
  main main_2 (.in_1(in_1), .in_2(in_2), .in_3(in_3), .in_4(in_4[1]), .out_6(out_6[1]), .in_5(in_5));
endmodule

// AM 1x4
module RAM_1x4 (
  input  in_1,
  input  in_2,
  input  in_3,
  input  [3:0] in_4,
  input  in_5,
  output [3:0] out_6
);

  RAM_1x2 ram_1x2_1 (.in_1(in_1), .in_2(in_2), .in_3(in_3), .in_4(in_4[1:0]), .out_6(out_6[1:0]), .in_5(in_5));
  RAM_1x2 ram_1x2_2 (.in_1(in_1), .in_2(in_2), .in_3(in_3), .in_4(in_4[3:2]), .out_6(out_6[3:2]), .in_5(in_5));
endmodule

// RAM 1X8
module RAM_1x8 (
  input  in_1,
  input  in_2,
  input  in_3,
  input  [7:0] in_4,
  input  in_5,
  output [7:0] out_6
);

  RAM_1x4 ram_1x4_1 (.in_1(in_1), .in_2(in_2), .in_4(in_4[3:0]), .out_6(out_6[3:0]), .in_5(in_5), .in_3(in_3));
  RAM_1x4 ram_1x4_2 (.in_1(in_1), .in_2(in_2), .in_4(in_4[7:4]), .out_6(out_6[7:4]), .in_5(in_5), .in_3(in_3));

  // Notes on the sheet:
  //   Rodolfo Herman - 451612
endmodule

module RAM_1x16 (
  input  ADDR,
  input  R___W,
  input  [15:0] in_3,
  input  CLEAR,
  output [15:0] out_5
);

  wire clock_1_out;

  Clock clock_1 (.out(clock_1_out));
  RAM_1x8 ram_1x8_1 (.in_1(ADDR), .in_2(R___W), .in_3(clock_1_out), .in_4(in_3[7:0]), .in_5(CLEAR), .out_6(out_5[7:0]));
  RAM_1x8 ram_1x8_2 (
    .in_1(ADDR), .in_2(R___W), .in_3(clock_1_out), .in_4(in_3[15:8]), .in_5(CLEAR), .out_6(out_5[15:8]));

  // Notes on the sheet:
  //   CLK
  //   DATA
  //   Rodolfo Herman - 451612
  //   SAIDA
endmodule
