// Logisim project Exercicio01.circ as structural Verilog: 3 circuits, main circuit main
module main (
  input  ADDR,
  input  R_W,
  input  CLK,
  input  IN_0,
  input  IN_1,
  input  IN_2,
  input  IN_3,
  input  CLR,
  output out_9,
  output out_10,
  output out_11,
  output out_12
);

  _1x2 u_1x2_1 (.ADDR(ADDR), .R_W(R_W), .CLK(CLK), .IN_0(IN_0), .IN_1(IN_1), .CLR(CLR), .OUT_0(out_9), .OUT_1(out_10));
  _1x2 u_1x2_2 (.ADDR(ADDR), .R_W(R_W), .CLK(CLK), .IN_0(IN_2), .IN_1(IN_3), .CLR(CLR), .OUT_0(out_11), .OUT_1(out_12));

  // Notes on the sheet:
  //   Nome: Tiago Matta Machado Zaidan
  //   Matricula: 451620
  //   Exercicio01
endmodule

module _1x1 (
  input  Addr,
  input  R_W,
  input  CLK,
  input  IN,
  input  CLR,
  output out_6
);

  wire and_1_out, j_k_ff_1_q, not_1_out;

  and and_1 (and_1_out, Addr, R_W, CLK);
  not not_1 (not_1_out, IN);
  J_K_Flip_Flop j_k_ff_1 (.J(IN), .clk(and_1_out), .K(not_1_out), .Q(j_k_ff_1_q), .reset(CLR));  // open: Qn, preset, en
  and and_2 (out_6, Addr, j_k_ff_1_q);
endmodule

module _1x2 (
  input  ADDR,
  input  R_W,
  input  CLK,
  input  IN_0,
  input  IN_1,
  input  CLR,
  output OUT_0,
  output OUT_1
);

  _1x1 u_1x1_1 (.Addr(ADDR), .R_W(R_W), .CLK(CLK), .IN(IN_0), .CLR(CLR), .out_6(OUT_0));
  _1x1 u_1x1_2 (.Addr(ADDR), .R_W(R_W), .CLK(CLK), .IN(IN_1), .CLR(CLR), .out_6(OUT_1));
endmodule
