// Logisim project Exercicio04.circ as structural Verilog: 5 circuits, main circuit main
module main (
  input  ADDR,
  input  R_W,
  input  CLK,
  input  [7:0] in_4,
  input  CLR,
  output [7:0] out_6
);

  _2x4 u_2x4_1 (
    .ADDR(ADDR), .R_W(R_W), .CLK(CLK), .IN_0(in_4[0]), .IN_1(in_4[1]), .IN_2(in_4[2]), .IN_3(in_4[3]),
    .CLR(CLR), .out_9(out_6[3:0]));
  _2x4 u_2x4_2 (
    .ADDR(ADDR), .R_W(R_W), .CLK(CLK), .IN_0(in_4[4]), .IN_1(in_4[5]), .IN_2(in_4[6]), .IN_3(in_4[7]),
    .CLR(CLR), .out_9(out_6[7:4]));

  // Notes on the sheet:
  //   Nome: Tiago Matta Machado Zaidan
  //   Matricula: 451620
  //   Exercicio04
endmodule

module _1x1 (
  input  Addr,
  input  R_W,
  input  CLK,
  input  IN,
  input  CLR,
  output out_6
);

  wire and_1_out, j_k_ff_1_q, not_1_out;

  and and_1 (and_1_out, Addr, R_W, CLK);
  not not_1 (not_1_out, IN);
  J_K_Flip_Flop j_k_ff_1 (.J(IN), .clk(and_1_out), .K(not_1_out), .Q(j_k_ff_1_q), .reset(CLR));  // open: Qn, preset, en
  and and_2 (out_6, Addr, j_k_ff_1_q);
endmodule

module _1x2 (
  input  ADDR,
  input  R_W,
  input  CLK,
  input  IN_0,
  input  IN_1,
  input  CLR,
  output OUT_0,
  output OUT_1
);

  _1x1 u_1x1_1 (.Addr(ADDR), .R_W(R_W), .CLK(CLK), .IN(IN_0), .CLR(CLR), .out_6(OUT_0));
  _1x1 u_1x1_2 (.Addr(ADDR), .R_W(R_W), .CLK(CLK), .IN(IN_1), .CLR(CLR), .out_6(OUT_1));
endmodule

module _1x4 (
  input  ADDR,
  input  R_W,
  input  CLK,
  input  IN_0,
  input  IN_1,
  input  IN_2,
  input  IN_3,
  input  CLR,
  output out_9,
  output out_10,
  output out_11,
  output out_12
);

  _1x2 u_1x2_1 (.ADDR(ADDR), .R_W(R_W), .CLK(CLK), .IN_0(IN_0), .IN_1(IN_1), .CLR(CLR), .OUT_0(out_9), .OUT_1(out_10));
  _1x2 u_1x2_2 (.ADDR(ADDR), .R_W(R_W), .CLK(CLK), .IN_0(IN_2), .IN_1(IN_3), .CLR(CLR), .OUT_0(out_11), .OUT_1(out_12));
endmodule

module _2x4 (
  input  ADDR,
  input  R_W,
  input  CLK,
  input  IN_0,
  input  IN_1,
  input  IN_2,
  input  IN_3,
  input  CLR,
  output [3:0] out_9
);

  wire demultiplexer_1_out0, demultiplexer_1_out1;
  wire [3:0] n1x4_1_out_9, n1x4_2_out_9;

  Demultiplexer demultiplexer_1 (
    .out0(demultiplexer_1_out0), .out1(demultiplexer_1_out1), .in(1'b1), .sel(ADDR));  // open: en
  _1x4 u_1x4_1 (
    .ADDR(demultiplexer_1_out0), .R_W(R_W), .CLK(CLK), .IN_0(IN_0), .IN_1(IN_1), .IN_2(IN_2), .IN_3(IN_3),
    .CLR(CLR), .out_9(n1x4_1_out_9[0]), .out_10(n1x4_1_out_9[1]), .out_11(n1x4_1_out_9[2]),
    .out_12(n1x4_1_out_9[3]));
  _1x4 u_1x4_2 (
    .ADDR(demultiplexer_1_out1), .R_W(R_W), .CLK(CLK), .IN_0(IN_0), .IN_1(IN_1), .IN_2(IN_2), .IN_3(IN_3),
    .CLR(CLR), .out_9(n1x4_2_out_9[0]), .out_10(n1x4_2_out_9[1]), .out_11(n1x4_2_out_9[2]),
    .out_12(n1x4_2_out_9[3]));
  Multiplexer #(.width(4)) multiplexer_1 (.in0(n1x4_1_out_9), .in1(n1x4_2_out_9), .out(out_9), .sel(ADDR));  // open: en
endmodule
