// Logisim project EX1.circ as structural Verilog: 1 circuit, main circuit main
module main (
  input  CLK,
  input  [3:0] INPUT,
  input  CLEAR,
  input  R_W,
  input  addr,
  output [3:0] OUTPUT
);

  wire and_1_out, not_1_out, not_2_out, not_3_out, not_4_out;

  and and_1 (and_1_out, CLK, R_W, addr);
  not not_1 (not_1_out, INPUT[3]);
  J_K_Flip_Flop j_k_ff_1 (
    .J(INPUT[3]), .clk(and_1_out), .K(not_1_out), .Q(OUTPUT[3]), .reset(CLEAR));  // open: Qn, preset, en
  J_K_Flip_Flop j_k_ff_2 (
    .J(INPUT[2]), .clk(and_1_out), .K(not_2_out), .Q(OUTPUT[2]), .reset(CLEAR));  // open: Qn, preset, en
  not not_2 (not_2_out, INPUT[2]);
  not not_3 (not_3_out, INPUT[1]);
  J_K_Flip_Flop j_k_ff_3 (
    .J(INPUT[1]), .clk(and_1_out), .K(not_3_out), .Q(OUTPUT[1]), .reset(CLEAR));  // open: Qn, preset, en
  not not_4 (not_4_out, INPUT[0]);
  J_K_Flip_Flop j_k_ff_4 (
    .J(INPUT[0]), .clk(and_1_out), .K(not_4_out), .Q(OUTPUT[0]), .reset(CLEAR));  // open: Qn, preset, en
endmodule
