// Logisim project EX3.circ as structural Verilog: 1 circuit, main circuit main
module main (
  input  CLK,
  input  [3:0] INPUT,
  input  CLEAR,
  input  R_W,
  input  addr,
  input  CLEAR_2,
  output [3:0] out_7
);

  wire and_1_out, and_2_out, not_1_out, not_2_out, not_3_out, not_4_out, not_5_out, not_6_out, not_7_out,
       not_8_out, not_9_out;
  wire [3:0] j_k_ff_7_q, j_k_ff_8_q;

  not not_1 (not_1_out, addr);
  and and_1 (and_1_out, CLK, R_W, addr);
  not not_2 (not_2_out, INPUT[3]);
  and and_2 (and_2_out, CLK, R_W, not_1_out);
  not not_3 (not_3_out, INPUT[3]);
  J_K_Flip_Flop j_k_ff_1 (
    .J(INPUT[3]), .clk(and_2_out), .K(not_2_out), .Q(j_k_ff_8_q[3]), .reset(CLEAR));  // open: Qn, preset, en
  J_K_Flip_Flop j_k_ff_2 (
    .J(INPUT[3]), .clk(and_1_out), .K(not_3_out), .Q(j_k_ff_7_q[3]), .reset(CLEAR_2));  // open: Qn, preset, en
  J_K_Flip_Flop j_k_ff_3 (
    .J(INPUT[2]), .clk(and_2_out), .K(not_4_out), .Q(j_k_ff_8_q[2]), .reset(CLEAR));  // open: Qn, preset, en
  not not_4 (not_4_out, INPUT[2]);
  J_K_Flip_Flop j_k_ff_4 (
    .J(INPUT[2]), .clk(and_1_out), .K(not_5_out), .Q(j_k_ff_7_q[2]), .reset(CLEAR_2));  // open: Qn, preset, en
  not not_5 (not_5_out, INPUT[2]);
  not not_6 (not_6_out, INPUT[1]);
  not not_7 (not_7_out, INPUT[1]);
  J_K_Flip_Flop j_k_ff_5 (
    .J(INPUT[1]), .clk(and_2_out), .K(not_6_out), .Q(j_k_ff_8_q[1]), .reset(CLEAR));  // open: Qn, preset, en
  J_K_Flip_Flop j_k_ff_6 (
    .J(INPUT[1]), .clk(and_1_out), .K(not_7_out), .Q(j_k_ff_7_q[1]), .reset(CLEAR_2));  // open: Qn, preset, en
  not not_8 (not_8_out, INPUT[0]);
  J_K_Flip_Flop j_k_ff_7 (
    .J(INPUT[0]), .clk(and_1_out), .K(not_9_out), .Q(j_k_ff_7_q[0]), .reset(CLEAR_2));  // open: Qn, preset, en
  not not_9 (not_9_out, INPUT[0]);
  J_K_Flip_Flop j_k_ff_8 (
    .J(INPUT[0]), .clk(and_2_out), .K(not_8_out), .Q(j_k_ff_8_q[0]), .reset(CLEAR));  // open: Qn, preset, en
  Multiplexer #(.width(4)) multiplexer_1 (.in0(j_k_ff_8_q), .in1(j_k_ff_7_q), .out(out_7), .sel(addr));  // open: en
endmodule
