// Logisim project EstudoDirigido10.circ as structural Verilog
// 1x4
module Exercicio01 (
  input  [3:0] Input,
  input  Clock,
  input  ADDR,
  input  R_W,
  input  CLR,
  output [3:0] Output
);

  wire and_1_out, not_1_out, not_2_out, not_3_out, not_4_out;

  and and_1 (and_1_out, Clock, ADDR, R_W);
  not not_1 (not_1_out, Input[3]);
  J_K_Flip_Flop j_k_ff_1 (
    .J(Input[3]), .clk(and_1_out), .K(not_1_out), .Q(Output[3]), .reset(CLR));  // open: Qn, preset, en
  J_K_Flip_Flop j_k_ff_2 (
    .J(Input[2]), .clk(and_1_out), .K(not_2_out), .Q(Output[2]), .reset(CLR));  // open: Qn, preset, en
  not not_2 (not_2_out, Input[2]);
  not not_3 (not_3_out, Input[1]);
  J_K_Flip_Flop j_k_ff_3 (
    .J(Input[1]), .clk(and_1_out), .K(not_3_out), .Q(Output[1]), .reset(CLR));  // open: Qn, preset, en
  J_K_Flip_Flop j_k_ff_4 (
    .J(Input[0]), .clk(and_1_out), .K(not_4_out), .Q(Output[0]), .reset(CLR));  // open: Qn, preset, en
  not not_4 (not_4_out, Input[0]);

  // Notes on the sheet:
  //   Wadson Ferreira - 460631
endmodule

// 2x4
module Exercicio02 (
  input  ADDR,
  input  Clock,
  input  R_W,
  input  [3:0] Input,
  input  CLR,
  output [3:0] Output
);

  wire not_1_out;
  wire [3:0] exercicio01_1_output, exercicio01_2_output;

  not not_1 (not_1_out, ADDR);
  Exercicio01 exercicio01_1 (
    .Clock(Clock), .ADDR(not_1_out), .R_W(R_W), .CLR(CLR), .Input(Input), .Output(exercicio01_1_output));
  assign Output = not_1_out ? exercicio01_1_output : 4'bz;  // Controlled_Buffer controlled_buffer_1
  Exercicio01 exercicio01_2 (
    .Clock(Clock), .ADDR(ADDR), .R_W(R_W), .CLR(CLR), .Input(Input), .Output(exercicio01_2_output));
  assign Output = ADDR ? exercicio01_2_output : 4'bz;  // Controlled_Buffer controlled_buffer_2

  // Notes on the sheet:
  //   Wadson Ferreira - 460631
endmodule

// 1x8
module Exercicio03 (
  input  ADDR,
  input  Clock,
  input  R_W,
  input  [7:0] Input,
  input  CLR,
  output [7:0] Output
);

  Exercicio01 exercicio01_1 (
    .Clock(Clock), .ADDR(ADDR), .R_W(R_W), .CLR(CLR), .Input(Input[7:4]), .Output(Output[7:4]));
  Exercicio01 exercicio01_2 (
    .Clock(Clock), .ADDR(ADDR), .R_W(R_W), .CLR(CLR), .Input(Input[3:0]), .Output(Output[3:0]));

  // Notes on the sheet:
  //   Wadson Ferreira - 460631
endmodule

// 2x8
module Exercicio04 (
  input  ADDR,
  input  Clock,
  input  RW,
  input  [7:0] Input,
  input  CLR,
  output [7:0] Output
);

  Exercicio02 exercicio02_1 (.ADDR(ADDR), .Clock(Clock), .R_W(RW), .Input(Input[7:4]), .CLR(CLR), .Output(Output[7:4]));
  Exercicio02 exercicio02_2 (.ADDR(ADDR), .Clock(Clock), .R_W(RW), .Input(Input[3:0]), .CLR(CLR), .Output(Output[3:0]));

  // Notes on the sheet:
  //   Wadson Ferreira - 460631
endmodule

// 1x16
module Exercicio06 (
  input  Addr,
  input  [15:0] Input,
  input  RW,
  input  Clock,
  output [15:0] out_5
);

  Exercicio03 exercicio03_1 (
    .ADDR(Addr), .Clock(Clock), .R_W(RW), .Input(Input[15:8]), .Output(out_5[15:8]));  // open: CLR
  Exercicio03 exercicio03_2 (
    .ADDR(Addr), .Clock(Clock), .R_W(RW), .Input(Input[7:0]), .Output(out_5[7:0]));  // open: CLR

  // Notes on the sheet:
  //   Wadson Ferreira - 460631
endmodule

module Exercicio07 (
  input  [1:0] Addr,
  input  [7:0] Input,
  input  Rw,
  output [7:0] out_4
);

  wire Clock_out, demultiplexer_1_out0, demultiplexer_1_out1, demultiplexer_1_out2, demultiplexer_1_out3;
  wire [7:0] exercicio03_1_output, exercicio03_2_output, exercicio03_3_output, exercicio03_4_output;

  Clock Clock (.out(Clock_out));
  Demultiplexer #(.select(2), .enable("false")) demultiplexer_1 (
    .out0(demultiplexer_1_out0), .out1(demultiplexer_1_out1), .out2(demultiplexer_1_out2),
    .out3(demultiplexer_1_out3), .in(1'b1), .sel(Addr));
  assign out_4 = demultiplexer_1_out0 ? exercicio03_1_output : 8'bz;  // Controlled_Buffer controlled_buffer_1
  Exercicio03 exercicio03_1 (
    .ADDR(demultiplexer_1_out0), .Clock(Clock_out), .R_W(Rw), .Input(Input), .Output(exercicio03_1_output));  // open: CLR
  Exercicio03 exercicio03_2 (
    .ADDR(demultiplexer_1_out1), .Clock(Clock_out), .R_W(Rw), .Input(Input), .Output(exercicio03_2_output));  // open: CLR
  Exercicio03 exercicio03_3 (
    .ADDR(demultiplexer_1_out2), .Clock(Clock_out), .R_W(Rw), .Input(Input), .Output(exercicio03_3_output));  // open: CLR
  Exercicio03 exercicio03_4 (
    .ADDR(demultiplexer_1_out3), .Clock(Clock_out), .R_W(Rw), .Input(Input), .Output(exercicio03_4_output));  // open: CLR
  assign out_4 = demultiplexer_1_out1 ? exercicio03_2_output : 8'bz;  // Controlled_Buffer controlled_buffer_2
  assign out_4 = demultiplexer_1_out2 ? exercicio03_3_output : 8'bz;  // Controlled_Buffer controlled_buffer_3
  assign out_4 = demultiplexer_1_out3 ? exercicio03_4_output : 8'bz;  // Controlled_Buffer controlled_buffer_4

  // Notes on the sheet:
  //   Wadson Ferreira - 460631
endmodule
