// Logisim project Ram 1x4.circ as structural Verilog: 1 circuit, main circuit main
module main (
  input  ADR,
  input  CLK,
  input  R_W,
  input  [3:0] DATA,
  input  CLR,
  output [3:0] out_6
);

  wire and_1_out, j_k_ff_1_q, j_k_ff_2_q, j_k_ff_3_q, j_k_ff_4_q, not_1_out, not_2_out, not_3_out, not_4_out;

  not not_1 (not_1_out, DATA[0]);
  and and_1 (and_1_out, ADR, CLK, R_W);
  J_K_Flip_Flop j_k_ff_1 (
    .J(DATA[0]), .clk(and_1_out), .K(not_1_out), .Q(j_k_ff_1_q), .reset(CLR));  // open: Qn, preset, en
  and and_2 (out_6[0], j_k_ff_1_q, ADR);
  and and_3 (out_6[1], j_k_ff_2_q, ADR);
  not not_2 (not_2_out, DATA[1]);
  and and_4 (out_6[3], ADR, j_k_ff_4_q);
  and and_5 (out_6[2], j_k_ff_3_q, ADR);
  J_K_Flip_Flop j_k_ff_2 (
    .J(DATA[1]), .clk(and_1_out), .K(not_2_out), .Q(j_k_ff_2_q), .reset(CLR));  // open: Qn, preset, en
  not not_3 (not_3_out, DATA[2]);
  J_K_Flip_Flop j_k_ff_3 (
    .J(DATA[2]), .clk(and_1_out), .K(not_3_out), .Q(j_k_ff_3_q), .reset(CLR));  // open: Qn, preset, en
  J_K_Flip_Flop j_k_ff_4 (
    .J(DATA[3]), .clk(and_1_out), .K(not_4_out), .Q(j_k_ff_4_q), .reset(CLR));  // open: Qn, preset, en
  not not_4 (not_4_out, DATA[3]);
endmodule
