// Logisim project Ram 1x8.circ as structural Verilog: 1 circuit, main circuit main
module main (
  input  in_1,
  input  in_2,
  input  [3:0] in_3,
  input  [3:0] in_4,
  input  in_5,
  output [3:0] out_6,
  output [3:0] out_7
);

  wire clock_1_out;

  Clock clock_1 (.out(clock_1_out));
  Ram_1x4_main main_1 (.ADR(in_1), .CLK(clock_1_out), .R_W(in_2), .DATA(in_3), .CLR(in_5), .out_6(out_7));
  Ram_1x4_main main_2 (.ADR(in_1), .CLK(clock_1_out), .R_W(in_2), .DATA(in_4), .CLR(in_5), .out_6(out_6));
endmodule
