// Logisim project Ram 2x4.circ as structural Verilog: 1 circuit, main circuit main
module main (
  input  in_1,
  input  in_2,
  input  [3:0] in_3,
  input  in_4,
  output [3:0] out_5
);

  wire clock_1_out, demultiplexer_1_out0, demultiplexer_1_out1;
  wire [3:0] main_1_out_6, main_2_out_6;

  Clock clock_1 (.out(clock_1_out));
  Demultiplexer #(.enable("false")) demultiplexer_1 (
    .out0(demultiplexer_1_out0), .out1(demultiplexer_1_out1), .in(1'b1), .sel(in_1));
  Ram_1x4_main main_1 (
    .ADR(demultiplexer_1_out0), .CLK(in_2), .R_W(clock_1_out), .DATA(in_3), .CLR(in_4), .out_6(main_1_out_6));
  Ram_1x4_main main_2 (
    .ADR(demultiplexer_1_out1), .CLK(in_2), .R_W(clock_1_out), .DATA(in_3), .CLR(in_4), .out_6(main_2_out_6));
  Multiplexer #(.width(4), .enable("false")) multiplexer_1 (
    .in0(main_1_out_6), .in1(main_2_out_6), .out(out_5), .sel(in_1));
endmodule
