// Logisim project Ram 4x8.circ as structural Verilog: 1 circuit, main circuit main
module main (
  input  [1:0] ADR,
  input  RW,
  input  CLK,
  input  CLR,
  input  [3:0] DATA,
  input  [3:0] in_6,
  output [3:0] out_7,
  output [3:0] out_8
);

  wire demultiplexer_1_out0, demultiplexer_1_out1, demultiplexer_1_out2, demultiplexer_1_out3;
  wire [3:0] main_1_out_6, main_2_out_6, main_3_out_6, main_4_out_6, main_5_out_6, main_6_out_6,
       main_7_out_6, main_8_out_6;

  Demultiplexer #(.select(2), .enable("false")) demultiplexer_1 (
    .out0(demultiplexer_1_out0), .out1(demultiplexer_1_out1), .out2(demultiplexer_1_out2),
    .out3(demultiplexer_1_out3), .in(1'b1), .sel(ADR));
  Ram_1x4_main main_1 (.ADR(demultiplexer_1_out0), .CLK(RW), .R_W(CLK), .DATA(DATA), .CLR(CLR), .out_6(main_1_out_6));
  Ram_1x4_main main_2 (.ADR(demultiplexer_1_out1), .CLK(RW), .R_W(CLK), .DATA(DATA), .CLR(CLR), .out_6(main_2_out_6));
  Ram_1x4_main main_3 (.ADR(demultiplexer_1_out2), .CLK(RW), .R_W(CLK), .DATA(DATA), .CLR(CLR), .out_6(main_3_out_6));
  Ram_1x4_main main_4 (.ADR(demultiplexer_1_out3), .CLK(RW), .R_W(CLK), .DATA(DATA), .CLR(CLR), .out_6(main_4_out_6));
  Multiplexer #(.select(2), .width(4), .enable("false")) multiplexer_1 (
    .in0(main_1_out_6), .in1(main_2_out_6), .in2(main_3_out_6), .in3(main_4_out_6), .out(out_7), .sel(ADR));
  Ram_1x4_main main_5 (.ADR(demultiplexer_1_out0), .CLK(RW), .R_W(CLK), .DATA(in_6), .CLR(CLR), .out_6(main_5_out_6));
  Ram_1x4_main main_6 (.ADR(demultiplexer_1_out1), .CLK(RW), .R_W(CLK), .DATA(in_6), .CLR(CLR), .out_6(main_6_out_6));
  Ram_1x4_main main_7 (.ADR(demultiplexer_1_out2), .CLK(RW), .R_W(CLK), .DATA(in_6), .CLR(CLR), .out_6(main_7_out_6));
  Ram_1x4_main main_8 (.ADR(demultiplexer_1_out3), .CLK(RW), .R_W(CLK), .DATA(in_6), .CLR(CLR), .out_6(main_8_out_6));
  Multiplexer #(.select(2), .width(4), .enable("false")) multiplexer_2 (
    .in0(main_5_out_6), .in1(main_6_out_6), .in2(main_7_out_6), .in3(main_8_out_6), .out(out_8), .sel(ADR));
endmodule
