// Logisim project Ram 8x8.circ as structural Verilog: 1 circuit, main circuit main
module main (
  input  REG,
  input  [1:0] ADR,
  input  CLR,
  input  [3:0] DATA,
  input  [3:0] in_5,
  output [3:0] out_6,
  output [3:0] out_7
);

  wire CLK_out, demultiplexer_1_out0, demultiplexer_1_out1;
  wire [3:0] Reg_0_out_7, Reg_0_out_8, Reg_1_out_7, Reg_1_out_8;

  Demultiplexer #(.enable("false")) demultiplexer_1 (
    .out0(demultiplexer_1_out0), .out1(demultiplexer_1_out1), .in(1'b1), .sel(REG));
  Clock CLK (.out(CLK_out));
  Ram_4x8_main Reg_0 (
    .ADR(ADR), .RW(demultiplexer_1_out0), .CLK(CLK_out), .CLR(CLR), .in_6(in_5), .out_8(Reg_0_out_8),
    .DATA(DATA), .out_7(Reg_0_out_7));
  Ram_4x8_main Reg_1 (
    .ADR(ADR), .RW(demultiplexer_1_out1), .CLK(CLK_out), .CLR(CLR), .in_6(in_5), .out_8(Reg_1_out_8),
    .DATA(DATA), .out_7(Reg_1_out_7));
  Multiplexer #(.width(4), .enable("false")) multiplexer_1 (
    .in0(Reg_0_out_7), .in1(Reg_1_out_7), .out(out_6), .sel(REG));
  Multiplexer #(.width(4), .enable("false")) multiplexer_2 (
    .in0(Reg_0_out_8), .in1(Reg_1_out_8), .out(out_7), .sel(REG));
endmodule
