// Logisim project Circuitos.circ as structural Verilog: 13 circuits, main circuit main
// 1x1
module main (
  input  Addr,
  input  R_W,
  input  CLK,
  input  Clear,
  input  IN,
  output OUT
);

  wire and_1_out, j_k_ff_1_q;

  and and_1 (and_1_out, Addr, R_W, CLK);
  J_K_Flip_Flop j_k_ff_1 (.J(IN), .clk(and_1_out), .K(IN), .Q(j_k_ff_1_q), .reset(Clear));  // open: Qn, preset, en
  and and_2 (OUT, Addr, j_k_ff_1_q);
endmodule

// 1x4
module _1x1_4 (
  input  Addr,
  input  R_W,
  input  CLK,
  input  [3:0] IN,
  input  Clear,
  output [3:0] OUT
);

  main main_1 (.Addr(Addr), .R_W(R_W), .CLK(CLK), .IN(IN[0]), .Clear(Clear), .OUT(OUT[0]));
  main main_2 (.Addr(Addr), .R_W(R_W), .CLK(CLK), .IN(IN[1]), .Clear(Clear), .OUT(OUT[1]));
  main main_3 (.Addr(Addr), .R_W(R_W), .CLK(CLK), .IN(IN[2]), .Clear(Clear), .OUT(OUT[2]));
  main main_4 (.Addr(Addr), .R_W(R_W), .CLK(CLK), .IN(IN[3]), .Clear(Clear), .OUT(OUT[3]));
endmodule

module _1x4 (
  input  Addr,
  input  R_W,
  input  in_3,
  input  [3:0] IN,
  input  clear,
  output [3:0] OUT
);

  _1x1_4 u_1x1_4_1 (.Addr(Addr), .R_W(R_W), .CLK(in_3), .IN(IN), .Clear(clear), .OUT(OUT));
endmodule

// 2x4
module _2_1x4 (
  input  Addr,
  input  R_W,
  input  CLK,
  input  [3:0] IN,
  input  Clear,
  output [3:0] OUT
);

  wire demultiplexer_1_out0, demultiplexer_1_out1;
  wire [3:0] n1x4_1_out, n1x4_2_out;

  Demultiplexer demultiplexer_1 (
    .out0(demultiplexer_1_out0), .out1(demultiplexer_1_out1), .in(1'b1), .sel(Addr));  // open: en
  _1x4 u_1x4_1 (.Addr(demultiplexer_1_out0), .R_W(R_W), .in_3(CLK), .IN(IN), .clear(Clear), .OUT(n1x4_1_out));
  _1x4 u_1x4_2 (.Addr(demultiplexer_1_out1), .R_W(R_W), .in_3(CLK), .IN(IN), .clear(Clear), .OUT(n1x4_2_out));
  Multiplexer #(.width(4)) multiplexer_1 (.in0(n1x4_1_out), .in1(n1x4_2_out), .out(OUT), .sel(Addr));  // open: en
endmodule

module _2x4 (
  input  Addr,
  input  R_W,
  input  CLK,
  input  [3:0] IN,
  input  Clear,
  output [3:0] OUT
);

  _2_1x4 u_2_1x4_1 (.Addr(Addr), .R_W(R_W), .CLK(CLK), .IN(IN), .Clear(Clear), .OUT(OUT));
endmodule

// 1x8
module _1x4_2 (
  input  Addr,
  input  R_W,
  input  CLK,
  input  [7:0] IN,
  input  clear,
  output [7:0] OUT
);

  _1x4 u_1x4_1 (.Addr(Addr), .R_W(R_W), .in_3(CLK), .IN(IN[3:0]), .clear(clear), .OUT(OUT[3:0]));
  _1x4 u_1x4_2 (.Addr(Addr), .R_W(R_W), .in_3(CLK), .IN(IN[7:4]), .clear(clear), .OUT(OUT[7:4]));
endmodule

module _1x8 (
  input  Addr,
  input  R_W,
  input  CLK,
  input  [7:0] IN,
  input  in_5,
  output [7:0] OUT
);

  _1x4_2 u_1x4_2_1 (.Addr(Addr), .R_W(R_W), .CLK(CLK), .IN(IN), .clear(in_5), .OUT(OUT));
endmodule

// 2x8
module _2x4_2 (
  input  Addr,
  input  R_W,
  input  CLK,
  input  [7:0] IN,
  input  in_5,
  output [7:0] OUT
);

  wire demultiplexer_1_out0, demultiplexer_1_out1;
  wire [3:0] n2x4_1_out, n2x4_2_out, n2x4_3_out, n2x4_4_out;

  Demultiplexer demultiplexer_1 (
    .out0(demultiplexer_1_out0), .out1(demultiplexer_1_out1), .in(1'b1), .sel(Addr));  // open: en
  _2x4 u_2x4_1 (.Addr(demultiplexer_1_out0), .R_W(R_W), .CLK(CLK), .IN(IN[3:0]), .Clear(in_5), .OUT(n2x4_1_out));
  _2x4 u_2x4_2 (.Addr(demultiplexer_1_out0), .R_W(R_W), .CLK(CLK), .IN(IN[7:4]), .Clear(in_5), .OUT(n2x4_2_out));
  _2x4 u_2x4_3 (.Addr(demultiplexer_1_out1), .R_W(R_W), .CLK(CLK), .IN(IN[3:0]), .Clear(in_5), .OUT(n2x4_3_out));
  _2x4 u_2x4_4 (.Addr(demultiplexer_1_out1), .R_W(R_W), .CLK(CLK), .IN(IN[7:4]), .Clear(in_5), .OUT(n2x4_4_out));
  Multiplexer #(.width(8)) multiplexer_1 (
    .in0({n2x4_2_out, n2x4_1_out}), .in1({n2x4_4_out, n2x4_3_out}), .out(OUT), .sel(Addr));  // open: en
endmodule

module _2x8 (
  input  Addr,
  input  R_W,
  input  CLK,
  input  [7:0] IN,
  input  Clear,
  output [7:0] OUT
);

  _2x4_2 u_2x4_2_1 (.Addr(Addr), .R_W(R_W), .CLK(CLK), .IN(IN), .in_5(Clear), .OUT(OUT));
endmodule

// 1x16
module _1x8_2 (
  input  Addr,
  input  R_W,
  input  CLK,
  input  [15:0] IN,
  input  Clear,
  output [15:0] OUT
);

  _1x8 u_1x8_1 (.Addr(Addr), .R_W(R_W), .CLK(CLK), .IN(IN[7:0]), .in_5(Clear), .OUT(OUT[7:0]));
  _1x8 u_1x8_2 (.Addr(Addr), .R_W(R_W), .CLK(CLK), .IN(IN[15:8]), .in_5(Clear), .OUT(OUT[15:8]));
endmodule

module _1x16 (
  input  Addr,
  input  R_W,
  input  CLK,
  input  [15:0] IN,
  input  Clear,
  output [15:0] OUT
);

  _1x8_2 u_1x8_2_1 (.Addr(Addr), .R_W(R_W), .CLK(CLK), .IN(IN), .Clear(Clear), .OUT(OUT));
endmodule

// 4x8
module _4_1x8 (
  input  [1:0] Addr,
  input  R_W,
  input  CLK,
  input  [7:0] IN,
  input  Clear,
  input  [3:0] in_6,
  input  [1:0] in_7,
  output [7:0] OUT,
  output [3:0] out_9
);

  wire demultiplexer_1_out0, demultiplexer_1_out1, demultiplexer_1_out2, demultiplexer_1_out3, not_1_out,
       not_2_out, not_3_out, not_4_out;
  wire [7:0] n1x8_1_out, n1x8_2_out, n1x8_3_out, n1x8_4_out;

  Demultiplexer #(.select(2)) demultiplexer_1 (
    .out0(demultiplexer_1_out0), .out1(demultiplexer_1_out1), .out2(demultiplexer_1_out2),
    .out3(demultiplexer_1_out3), .in(1'b1), .sel(Addr));  // open: en
  _1x8 u_1x8_1 (.Addr(demultiplexer_1_out0), .R_W(R_W), .CLK(CLK), .IN(IN), .in_5(Clear), .OUT(n1x8_1_out));
  _1x8 u_1x8_2 (.Addr(demultiplexer_1_out1), .R_W(R_W), .CLK(CLK), .IN(IN), .in_5(Clear), .OUT(n1x8_2_out));
  _1x8 u_1x8_3 (.Addr(demultiplexer_1_out2), .R_W(R_W), .CLK(CLK), .IN(IN), .in_5(Clear), .OUT(n1x8_3_out));
  _1x8 u_1x8_4 (.Addr(demultiplexer_1_out3), .R_W(R_W), .CLK(CLK), .IN(IN), .in_5(Clear), .OUT(n1x8_4_out));
  Multiplexer #(.select(2), .width(8)) multiplexer_1 (
    .in0(n1x8_1_out), .in1(n1x8_2_out), .in2(n1x8_3_out), .in3(n1x8_4_out), .out(OUT), .sel(Addr));  // open: en
  not not_1 (not_1_out, in_7[0]);
  not not_2 (not_2_out, in_7[1]);
  not not_3 (not_3_out, in_7[0]);
  not not_4 (not_4_out, in_7[1]);
  and and_1 (out_9[0], in_6[0], in_7[0], in_7[1]);
  and and_2 (out_9[1], in_6[1], not_1_out, in_7[1]);
  and and_3 (out_9[2], in_6[2], in_7[0], not_2_out);
  and and_4 (out_9[3], in_6[3], not_3_out, not_4_out);
endmodule

module _4x8 (
  input  [1:0] Addr,
  input  R_W,
  input  CLK,
  input  [7:0] IN,
  input  Clear,
  output [7:0] OUT
);

  // _4_1x8 4_1x8_1: pin names not known; wires that end beside it: Addr, R_W, CLK, IN, Clear, OUT
endmodule
