// Logisim project Circuito_Guia10.circ as structural Verilog: 7 circuits, main circuit Exercicio10_01
// 4x1
module Exercicio10_01 (
  input  ADDR,
  input  R___W,
  input  Clock,
  input  [3:0] IMP,
  input  Clear,
  output [3:0] OUT
);

  wire and_1_out, not_1_out, not_2_out, not_3_out, not_4_out;
  wire [3:0] j_k_ff_4_q;

  and and_1 (and_1_out, Clock, R___W, ADDR);
  J_K_Flip_Flop j_k_ff_1 (
    .J(IMP[3]), .clk(and_1_out), .K(not_1_out), .Q(j_k_ff_4_q[3]), .reset(Clear));  // open: Qn, preset, en
  not not_1 (not_1_out, IMP[3]);
  not not_2 (not_2_out, IMP[2]);
  J_K_Flip_Flop j_k_ff_2 (
    .J(IMP[2]), .clk(and_1_out), .K(not_2_out), .Q(j_k_ff_4_q[2]), .reset(Clear));  // open: Qn, preset, en
  J_K_Flip_Flop j_k_ff_3 (
    .J(IMP[1]), .clk(and_1_out), .K(not_3_out), .Q(j_k_ff_4_q[1]), .reset(Clear));  // open: Qn, preset, en
  not not_3 (not_3_out, IMP[1]);
  not not_4 (not_4_out, IMP[0]);
  J_K_Flip_Flop j_k_ff_4 (
    .J(IMP[0]), .clk(and_1_out), .K(not_4_out), .Q(j_k_ff_4_q[0]), .reset(Clear));  // open: Qn, preset, en
  assign OUT = j_k_ff_4_q & {4{ADDR}};  // AND_Gate and_2, 4 bits wide
endmodule

// 2x4
module Exercicio10_02 (
  input  ADDR,
  input  R___W,
  input  Clock,
  input  [3:0] INP,
  input  Clear,
  output [3:0] OUT
);

  wire demultiplexer_1_out0, demultiplexer_1_out1;
  wire [3:0] exercicio10_01_1_out, undriven;

  Demultiplexer #(.enable("false")) demultiplexer_1 (
    .out0(demultiplexer_1_out0), .out1(demultiplexer_1_out1), .in(1'b1), .sel(ADDR));
  Exercicio10_01 exercicio10_01_1 (
    .ADDR(demultiplexer_1_out0), .R___W(R___W), .Clock(Clock), .Clear(Clear), .OUT(exercicio10_01_1_out));  // open: IMP
  Exercicio10_01 exercicio10_01_2 (
    .ADDR(demultiplexer_1_out1), .R___W(R___W), .Clock(Clock), .Clear(Clear), .IMP(undriven), .OUT(INP));
  Multiplexer #(.width(4), .enable("false")) multiplexer_1 (
    .in0(exercicio10_01_1_out), .in1(undriven), .out(OUT), .sel(ADDR));
endmodule

// 1x8
module Exercicio10_03 (
  input  Clock,
  input  [7:0] INPUT,
  input  R___W,
  input  ADDR,
  input  Clear,
  output [7:0] OUTPUT
);

  Exercicio10_01 exercicio10_01_1 (
    .ADDR(Clock), .Clock(R___W), .Clear(Clear), .IMP(INPUT[3:0]), .OUT(OUTPUT[3:0]));  // open: R___W
  Exercicio10_01 exercicio10_01_2 (
    .ADDR(Clock), .Clock(R___W), .Clear(Clear), .IMP(INPUT[7:4]), .OUT(OUTPUT[7:4]));  // open: R___W
endmodule

// 2X8
module Exercicio10_04 (
  input  Clock,
  input  [7:0] INPUT,
  input  R___W,
  input  ADDR,
  input  Clear,
  output [7:0] OUTPUT
);

  wire exercicio10_02_2_p6, exercicio10_02_2_p8;

  // Exercicio10_02 exercicio10_02_1: pin names not known; wires that end beside it: Clock, R___W, ADDR, {INPUT[7:5], Clear}, INPUT[3:0], OUTPUT[3:0]
  // Exercicio10_02 exercicio10_02_2: pin names not known; wires that end beside it: ADDR, Clock, R___W, ADDR, {INPUT[7:5], Clear}, exercicio10_02_2_p6, {INPUT[7:5], Clear}, exercicio10_02_2_p8
  Exercicio10_02 exercicio10_02_3 (
    .ADDR(exercicio10_02_2_p6), .R___W(exercicio10_02_2_p8), .INP({INPUT[7:5], Clear}),
    .OUT({INPUT[7:5], Clear}));  // open: Clock, Clear
  // Pins of 1 and 4 bits meet at {INPUT[7:5], Clear}

  assign INPUT[4] = Clear;
  assign OUTPUT[7:4] = {INPUT[7:5], Clear};
endmodule

module Exercicio10_05 (
  input  [2:0] ADDR,
  input  Clock,
  input  [7:0] INPUT,
  input  R___W,
  input  Clock_2,
  output [7:0] OUTPUT
);

  wire and_1_out, and_2_out, and_3_out, and_4_out, demultiplexer_1_out0, demultiplexer_1_out1,
       demultiplexer_1_out2, demultiplexer_1_out3;
  wire [7:0] exercicio10_04_1_output, exercicio10_04_2_output, exercicio10_04_3_output,
       exercicio10_04_4_output;

  Demultiplexer #(.select(2), .enable("false")) demultiplexer_1 (
    .out0(demultiplexer_1_out0), .out1(demultiplexer_1_out1), .out2(demultiplexer_1_out2),
    .out3(demultiplexer_1_out3), .in(1'b1), .sel(ADDR[1:0]));
  and and_1 (and_1_out, demultiplexer_1_out0, ADDR[2]);
  and and_2 (and_2_out, demultiplexer_1_out1, ADDR[2]);
  and and_3 (and_3_out, demultiplexer_1_out2, ADDR[2]);
  and and_4 (and_4_out, demultiplexer_1_out3, ADDR[2]);
  Exercicio10_04 exercicio10_04_1 (
    .Clock(Clock), .R___W(R___W), .ADDR(and_1_out), .Clear(Clock_2), .INPUT(INPUT),
    .OUTPUT(exercicio10_04_1_output));
  Exercicio10_04 exercicio10_04_2 (
    .Clock(Clock), .R___W(R___W), .ADDR(and_2_out), .Clear(Clock_2), .INPUT(INPUT),
    .OUTPUT(exercicio10_04_2_output));
  Exercicio10_04 exercicio10_04_3 (
    .Clock(Clock), .R___W(R___W), .ADDR(and_3_out), .Clear(Clock_2), .INPUT(INPUT),
    .OUTPUT(exercicio10_04_3_output));
  Exercicio10_04 exercicio10_04_4 (
    .Clock(Clock), .R___W(R___W), .ADDR(and_4_out), .Clear(Clock_2), .INPUT(INPUT),
    .OUTPUT(exercicio10_04_4_output));
  Multiplexer #(.select(2), .width(8), .enable("false")) multiplexer_1 (
    .in0(exercicio10_04_1_output), .in1(exercicio10_04_2_output), .in2(exercicio10_04_3_output),
    .in3(exercicio10_04_4_output), .out(OUTPUT), .sel(ADDR[1:0]));
endmodule

module Exercicio10_06 (
  input  Clock,
  input  [15:0] INPUT,
  input  R___W,
  input  ADDR,
  input  Clear,
  output [15:0] OUTPUT
);

  Exercicio10_03 exercicio10_03_1 (
    .Clock(Clock), .R___W(R___W), .ADDR(ADDR), .Clear(Clear), .INPUT(INPUT[7:0]), .OUTPUT(OUTPUT[7:0]));
  Exercicio10_03 exercicio10_03_2 (
    .Clock(Clock), .R___W(R___W), .ADDR(ADDR), .Clear(Clear), .INPUT(INPUT[15:8]), .OUTPUT(OUTPUT[15:8]));
endmodule

module Exercicio10_07 (
  input  [1:0] ADDR,
  input  Clock,
  input  [7:0] INP,
  input  R___W,
  input  Clk,
  output [7:0] OUT
);

  wire demultiplexer_1_out0, demultiplexer_1_out1, demultiplexer_1_out2, demultiplexer_1_out3;
  wire [7:0] exercicio10_03_1_output, exercicio10_03_2_output, exercicio10_03_3_output,
       exercicio10_03_4_output;

  Demultiplexer #(.select(2), .enable("false")) demultiplexer_1 (
    .out0(demultiplexer_1_out0), .out1(demultiplexer_1_out1), .out2(demultiplexer_1_out2),
    .out3(demultiplexer_1_out3), .in(1'b1), .sel(ADDR));
  Exercicio10_03 exercicio10_03_1 (
    .Clock(Clock), .R___W(R___W), .ADDR(demultiplexer_1_out0), .Clear(Clk), .INPUT(INP),
    .OUTPUT(exercicio10_03_1_output));
  Exercicio10_03 exercicio10_03_2 (
    .Clock(Clock), .R___W(R___W), .ADDR(demultiplexer_1_out1), .Clear(Clk), .INPUT(INP),
    .OUTPUT(exercicio10_03_2_output));
  Exercicio10_03 exercicio10_03_3 (
    .Clock(Clock), .R___W(R___W), .ADDR(demultiplexer_1_out2), .Clear(Clk), .INPUT(INP),
    .OUTPUT(exercicio10_03_3_output));
  Exercicio10_03 exercicio10_03_4 (
    .Clock(Clock), .R___W(R___W), .ADDR(demultiplexer_1_out3), .Clear(Clk), .INPUT(INP),
    .OUTPUT(exercicio10_03_4_output));
  Multiplexer #(.select(2), .width(8), .enable("false")) multiplexer_1 (
    .in0(exercicio10_03_1_output), .in1(exercicio10_03_2_output), .in2(exercicio10_03_3_output),
    .in3(exercicio10_03_4_output), .out(OUT), .sel(ADDR));
endmodule
