// Logisim project Exemplo0034.circ as structural Verilog: 1 circuit, main circuit main
module main (
  input  in_1,
  input  A,
  input  B,
  output out_4,
  output out_5,
  output out_6,
  output out_7
);

  wire nor_1_out, not_1_out, not_2_out, or_1_out, xnor_1_out, xor_1_out;

  xor xor_1 (xor_1_out, B, A);
  xnor xnor_1 (xnor_1_out, B, A);
  nor nor_1 (nor_1_out, B, A);
  or or_1 (or_1_out, B, A);
  not not_1 (not_1_out, in_1);
  and and_1 (out_5, xnor_1_out, not_2_out);
  not not_2 (not_2_out, in_1);
  and and_2 (out_4, xor_1_out, not_1_out);
  and and_3 (out_6, in_1, or_1_out);
  and and_4 (out_7, nor_1_out, in_1);
endmodule
