// Logisim project Exemplo0035.circ as structural Verilog: 1 circuit, main circuit main
module main (
  input  a,
  input  b,
  input  c3,
  input  c2,
  input  c1,
  output s
);

  wire AND1_out, AND2_out, AND3_out, AND4_out, AND5_out, AND6_out, AND7_out, AND8_out, NAND1_out, NOR_out,
       not_2_out, not_3_out, not_4_out, not_5_out, not_6_out, not_7_out, not_8_out, not_9_out, not_10_out,
       not_11_out, not_12_out, not_13_out, NOT_out, OR1_out, XNOR1_out, XOR1_out;

  not NOT (NOT_out, a);
  or OR1 (OR1_out, a, b);
  nor NOR (NOR_out, a, b);
  and AND1 (AND1_out, a, b);
  nand NAND1 (NAND1_out, a, b);
  xor XOR1 (XOR1_out, a, b);
  xnor XNOR1 (XNOR1_out, a, b);
  not not_2 (not_2_out, c3);
  not not_3 (not_3_out, c2);
  and AND2 (AND2_out, not_2_out, not_3_out, not_4_out, NOT_out);
  not not_4 (not_4_out, c1);
  not not_5 (not_5_out, c3);
  not not_6 (not_6_out, c2);
  and AND3 (AND3_out, not_5_out, not_6_out, c1, OR1_out);
  not not_7 (not_7_out, c3);
  not not_8 (not_8_out, c1);
  and AND4 (AND4_out, not_7_out, c2, not_8_out, NOR_out);
  not not_9 (not_9_out, c3);
  and AND5 (AND5_out, not_9_out, c2, c1, AND1_out);
  not not_10 (not_10_out, c2);
  and AND6 (AND6_out, c3, not_10_out, not_11_out, NAND1_out);
  not not_11 (not_11_out, c1);
  not not_12 (not_12_out, c2);
  and AND7 (AND7_out, c3, not_12_out, c1, XOR1_out);
  not not_13 (not_13_out, c1);
  and AND8 (AND8_out, c3, c2, not_13_out, XNOR1_out);
  or OR2 (s, AND2_out, AND3_out, AND4_out, AND5_out, AND6_out, AND7_out, AND8_out);
endmodule
