// Logisim project Exemplo0035c.circ as structural Verilog: 1 circuit, main circuit main
module main (
  input  [2:0] in_1,
  input  in_2,
  input  in_3,
  output out_4
);

  wire and_1_out, and_2_out, and_3_out, and_4_out, and_5_out, and_6_out, and_7_out, and_8_out, and_9_out,
       and_10_out, and_11_out, and_12_out, and_13_out, and_14_out, not_1_out, not_2_out, not_3_out,
       not_4_out, not_5_out, not_6_out, not_7_out, not_8_out, not_9_out, or_1_out, or_2_out, or_3_out,
       or_4_out, or_5_out, or_6_out, or_7_out;

  not not_1 (not_1_out, in_1[1]);
  not not_2 (not_2_out, in_1[2]);
  not not_3 (not_3_out, in_1[0]);
  and and_1 (and_1_out, in_3, in_1[0], in_2);
  not not_4 (not_4_out, in_2);
  not not_5 (not_5_out, in_3);
  not not_6 (not_6_out, in_3);
  not not_7 (not_7_out, in_2);
  or or_1 (or_1_out, in_3, and_1_out, in_2);
  or or_2 (or_2_out, not_3_out, and_1_out);
  and and_2 (and_2_out, in_3, not_4_out);
  and and_3 (and_3_out, not_5_out, in_2);
  and and_4 (and_4_out, not_6_out, not_3_out);
  and and_5 (and_5_out, in_1[0], not_7_out);
  and and_6 (and_6_out, or_1_out, or_2_out);
  or or_3 (or_3_out, and_2_out, and_3_out);
  or or_4 (or_4_out, and_4_out, and_5_out);
  not not_8 (not_8_out, and_6_out);
  and and_7 (and_7_out, or_3_out, not_3_out);
  and and_8 (and_8_out, in_1[0], not_9_out);
  not not_9 (not_9_out, or_3_out);
  and and_9 (and_9_out, in_1[1], or_4_out);
  and and_10 (and_10_out, and_6_out, not_1_out);
  or or_5 (or_5_out, and_10_out, and_11_out);
  and and_11 (and_11_out, in_1[1], not_8_out);
  or or_6 (or_6_out, and_7_out, and_8_out);
  and and_12 (and_12_out, or_6_out, not_1_out);
  or or_7 (or_7_out, and_12_out, and_9_out);
  and and_13 (and_13_out, or_5_out, not_2_out);
  or or_8 (out_4, and_13_out, and_14_out);
  and and_14 (and_14_out, in_1[2], or_7_out);
endmodule
