// Logisim project Exemplo0036.circ as structural Verilog: 1 circuit, main circuit main
module main (
  input  in_1,
  input  in_2,
  input  in_3,
  output out_4
);

  wire and_1_out, and_2_out, not_1_out, xnor_1_out, xor_1_out;

  not not_1 (not_1_out, in_1);
  xor xor_1 (xor_1_out, in_3, in_2);
  xnor xnor_1 (xnor_1_out, in_3, in_2);
  and and_1 (and_1_out, xor_1_out, not_1_out);
  and and_2 (and_2_out, in_1, xnor_1_out);
  or or_1 (out_4, and_1_out, and_2_out);
endmodule
