// Logisim project Circ Exemplo0035.circ as structural Verilog: 1 circuit, main circuit main
module main (
  input  [2:0] CHAVE,
  input  A,
  input  B,
  output s
);

  wire AND1_out, AND_2_out, AND_3_out, AND_4_out, AND_5_out, AND_6_out, AND_7_out, AND_8_out, AND_9_out,
       NAND_out, NOR_out, not_1_out, not_2_out, not_3_out, not_4_out, not_5_out, not_6_out, not_7_out,
       not_8_out, not_9_out, not_10_out, not_11_out, not_12_out, not_13_out, NOT_A_out, OR_out, XNOR_out,
       XOR_out;

  not NOT_A (NOT_A_out, A);
  not not_1 (not_1_out, B);
  xor XOR (XOR_out, B, A);
  or OR (OR_out, B, A);
  and AND1 (AND1_out, B, A);
  xnor XNOR (XNOR_out, B, A);
  nor NOR (NOR_out, B, A);
  nand NAND (NAND_out, B, A);
  not not_2 (not_2_out, CHAVE[0]);
  not not_3 (not_3_out, CHAVE[1]);
  not not_4 (not_4_out, CHAVE[2]);
  not not_5 (not_5_out, CHAVE[1]);
  not not_6 (not_6_out, CHAVE[2]);
  not not_7 (not_7_out, CHAVE[0]);
  not not_8 (not_8_out, CHAVE[2]);
  not not_9 (not_9_out, CHAVE[2]);
  not not_10 (not_10_out, CHAVE[0]);
  not not_11 (not_11_out, CHAVE[1]);
  not not_12 (not_12_out, CHAVE[0]);
  not not_13 (not_13_out, CHAVE[0]);
  and AND_2 (AND_2_out, XOR_out, not_2_out, not_3_out, not_4_out);
  and AND_3 (AND_3_out, OR_out, CHAVE[0], not_5_out, not_6_out);
  and AND_4 (AND_4_out, AND1_out, not_7_out, CHAVE[1], not_8_out);
  and AND_5 (AND_5_out, XNOR_out, CHAVE[0], CHAVE[1], not_9_out);
  and AND_6 (AND_6_out, NOR_out, not_10_out, not_11_out, CHAVE[2]);
  and AND_7 (AND_7_out, NAND_out, CHAVE[0], not_12_out, CHAVE[2]);
  and AND_8 (AND_8_out, NOT_A_out, not_13_out, CHAVE[1], CHAVE[2]);
  and AND_9 (AND_9_out, not_1_out, CHAVE[0], CHAVE[1], CHAVE[2]);
  or OR_2 (s, AND_2_out, AND_3_out, AND_4_out, AND_5_out, AND_6_out, AND_7_out, AND_8_out, AND_9_out);

  // Notes on the sheet:
  //   NOT B
  //   s1
  //   s2
  //   s3
  //   s4
  //   s5
  //   s6
  //   s7
  //   s8
  //   000  XOR
  //   001 OR
  //   010 AND
  //   011 XNOR
  //   100 NOR
  //   101 NAND
  //   110 NOT A
  //   111 NOT B
  //   s9
  //   s10
  //   s11
  //   s12
  //   s13
  //   s14
  //   s15
  //   s16
endmodule
