// Logisim project Exemplo0031.circ as structural Verilog: 1 circuit, main circuit main
module main (
  input  [3:0] X,
  input  [3:0] Y,
  output [3:0] out_3,
  output [3:0] out_4
);

  assign out_3 = Y & X;  // AND_Gate and_1, 4 bits wide
  assign out_4 = Y | X;  // OR_Gate or_1, 4 bits wide

  // Notes on the sheet:
  //   Rodolfo Herman - 451612
  //   Operações simultaneas com AND e OR
endmodule
