// Logisim project Exemplo0033.circ as structural Verilog: 1 circuit, main circuit main
module main (
  input  A,
  input  B,
  input  in_3,
  output out_4
);

  wire and_1_out, and_2_out, and_3_out, nand_1_out, nor_1_out, not_1_out, or_1_out, or_2_out, or_3_out;

  and and_1 (and_1_out, B, A);
  or or_1 (or_1_out, B, A);
  nand nand_1 (nand_1_out, B, A);
  nor nor_1 (nor_1_out, B, A);
  or or_2 (or_2_out, and_1_out, or_1_out);
  or or_3 (or_3_out, nand_1_out, nor_1_out);
  not not_1 (not_1_out, in_3);
  and and_2 (and_2_out, or_2_out, not_1_out);
  and and_3 (and_3_out, or_3_out, in_3);
  or or_4 (out_4, and_2_out, and_3_out);

  // Notes on the sheet:
  //   Rodolfo Herman - 451612
  //   0 - Grupo (AND/OR)
  //   1 - Grupo (NAND/NOR)
endmodule
