// Logisim project Exemplo0035.circ as structural Verilog: 1 circuit, main circuit main
module main (
  input  A,
  input  B,
  input  [2:0] in_3,
  output out_4
);

  wire and_1_out, and_2_out, and_3_out, and_4_out, and_5_out, and_6_out, and_7_out, and_8_out, and_9_out,
       nand_1_out, nor_1_out, not_1_out, not_2_out, not_3_out, not_4_out, not_5_out, not_6_out, not_7_out,
       not_8_out, not_9_out, not_10_out, not_11_out, not_12_out, not_13_out, not_14_out, or_1_out, or_2_out,
       or_3_out, or_4_out, or_5_out, or_6_out, or_7_out, xnor_1_out, xor_1_out;

  not not_1 (not_1_out, B);
  not not_2 (not_2_out, A);
  or or_1 (or_1_out, B, A);
  nor nor_1 (nor_1_out, B, A);
  and and_1 (and_1_out, B, A);
  nand nand_1 (nand_1_out, B, A);
  xor xor_1 (xor_1_out, B, A);
  xnor xnor_1 (xnor_1_out, B, A);
  not not_3 (not_3_out, in_3[0]);
  not not_4 (not_4_out, in_3[0]);
  not not_5 (not_5_out, in_3[1]);
  not not_6 (not_6_out, in_3[2]);
  not not_7 (not_7_out, in_3[1]);
  not not_8 (not_8_out, in_3[2]);
  not not_9 (not_9_out, in_3[0]);
  not not_10 (not_10_out, in_3[2]);
  not not_11 (not_11_out, in_3[2]);
  not not_12 (not_12_out, in_3[0]);
  not not_13 (not_13_out, in_3[1]);
  not not_14 (not_14_out, in_3[1]);
  and and_2 (and_2_out, not_1_out, not_3_out, in_3[1], in_3[2]);
  and and_3 (and_3_out, not_2_out, not_4_out, not_5_out, not_6_out);
  and and_4 (and_4_out, or_1_out, in_3[0], not_7_out, not_8_out);
  and and_5 (and_5_out, nor_1_out, not_9_out, in_3[1], not_10_out);
  and and_6 (and_6_out, and_1_out, in_3[0], in_3[1], not_11_out);
  and and_7 (and_7_out, nand_1_out, not_12_out, not_13_out, in_3[2]);
  and and_8 (and_8_out, xor_1_out, in_3[0], not_14_out, in_3[2]);
  and and_9 (and_9_out, xnor_1_out, in_3[0], in_3[1], in_3[2]);
  or or_2 (or_2_out, and_2_out, and_3_out);
  or or_3 (or_3_out, and_4_out, and_5_out);
  or or_4 (or_4_out, and_6_out, and_7_out);
  or or_5 (or_5_out, and_8_out, and_9_out);
  or or_6 (or_6_out, or_2_out, or_3_out);
  or or_7 (or_7_out, or_4_out, or_5_out);
  or or_8 (out_4, or_6_out, or_7_out);

  // Notes on the sheet:
  //   Rodolfo Herman - 451612
  //   000 - Porta NOT-A
  //   001 - Porta OR
  //   010 - Porta NOR
  //   011 - Porta AND
  //   100 - Porta NAND
  //   101 - Prota XOR
  //   110 - Porta NOT-B
  //   111 - Porta XNOR
endmodule
