// Logisim project Exemplo0031.circ as structural Verilog: 2 circuits, main circuit main
module main (
  input  [3:0] in_1,
  input  [3:0] in_2,
  output [3:0] out_3,
  output [3:0] out_4
);

  LU lu_1 (.in_1(in_1), .in_2(in_2), .out_3(out_3), .out_4(out_4));

  // Notes on the sheet:
  //   Exemplo0031
  //   Nome: Tiago Matta Machado Zaidan
  //   Matricula: 451620
endmodule

module LU (
  input  [3:0] in_1,
  input  [3:0] in_2,
  output [3:0] out_3,
  output [3:0] out_4
);

  assign out_3 = in_1 & in_2;  // AND_Gate and_1, 4 bits wide
  assign out_4 = in_1 | in_2;  // OR_Gate or_1, 4 bits wide
endmodule
