// Logisim project Exemplo0032.circ as structural Verilog: 2 circuits, main circuit main
module main (
  input  in_1,
  input  in_2,
  input  in_3,
  output out_4
);

  wire and_1_out, and_2_out, lu_1_out_3, lu_1_out_4, not_1_out;

  LU lu_1 (.in_1(in_1), .in_2(in_2), .out_3(lu_1_out_3), .out_4(lu_1_out_4));
  not not_1 (not_1_out, in_3);
  and and_1 (and_1_out, not_1_out, lu_1_out_3);
  and and_2 (and_2_out, lu_1_out_4, in_3);
  or or_1 (out_4, and_1_out, and_2_out);

  // Notes on the sheet:
  //   Exemplo0032
  //   Nome: Tiago Matta Machado Zaidan
  //   Matricula: 451620
  //   0 - or   /   1 - and
endmodule

module LU (
  input  in_1,
  input  in_2,
  output out_3,
  output out_4
);

  or or_1 (out_3, in_1, in_2);
  and and_1 (out_4, in_2, in_1);
endmodule
