// Logisim project Exemplo0033.circ as structural Verilog: 2 circuits, main circuit main
module main (
  input  in_1,
  input  in_2,
  input  in_3,
  output out_4,
  output out_5
);

  wire and_1_out, and_2_out, and_3_out, and_4_out, lu_1_out_3, lu_1_out_4, lu_1_out_5, lu_1_out_6, not_1_out;

  LU lu_1 (.in_1(in_1), .in_2(in_2), .out_3(lu_1_out_3), .out_4(lu_1_out_4), .out_5(lu_1_out_5), .out_6(lu_1_out_6));
  not not_1 (not_1_out, in_3);
  and and_1 (and_1_out, lu_1_out_3, not_1_out);
  and and_2 (and_2_out, lu_1_out_4, not_1_out);
  and and_3 (and_3_out, lu_1_out_5, in_3);
  and and_4 (and_4_out, lu_1_out_6, in_3);
  or or_1 (out_4, and_1_out, and_3_out);
  or or_2 (out_5, and_2_out, and_4_out);

  // Notes on the sheet:
  //   Exemplo0033
  //   Nome: Tiago Matta Machado Zaidan
  //   Matricula: 451620
endmodule

module LU (
  input  in_1,
  input  in_2,
  output out_3,
  output out_4,
  output out_5,
  output out_6
);

  or or_1 (out_3, in_1, in_2);
  and and_1 (out_4, in_1, in_2);
  nor nor_1 (out_5, in_1, in_2);
  nand nand_1 (out_6, in_1, in_2);
endmodule
