// Logisim project Exemplo0035.circ as structural Verilog: 1 circuit, main circuit main
module main (
  input  in_1,
  input  in_2,
  input  [2:0] in_3,
  output out_4
);

  wire and_1_out, and_2_out, and_3_out, and_4_out, and_5_out, and_6_out, not_1_out, not_2_out, not_3_out,
       not_4_out, not_5_out, not_6_out, not_7_out, not_8_out;

  not not_1 (not_1_out, in_1);
  not not_2 (not_2_out, in_2);
  not not_3 (not_3_out, in_3[0]);
  not not_4 (not_4_out, in_3[1]);
  not not_5 (not_5_out, in_2);
  not not_6 (not_6_out, in_3[2]);
  and and_1 (and_1_out, not_1_out, not_2_out, not_3_out);
  and and_2 (and_2_out, in_1, not_5_out, in_3[2], not_7_out);
  and and_3 (and_3_out, in_1, in_2, not_6_out, in_3[0]);
  not not_7 (not_7_out, in_3[1]);
  and and_4 (and_4_out, not_1_out, in_2, not_4_out);
  and and_5 (and_5_out, not_2_out, in_1, not_4_out, in_3[0]);
  not not_8 (not_8_out, in_3[0]);
  and and_6 (and_6_out, in_1, in_2, not_8_out, in_3[1], in_3[2]);
  or or_1 (out_4, and_1_out, and_4_out, and_5_out, and_6_out, and_2_out, and_3_out);

  // Notes on the sheet:
  //   Exemplo0035
  //   Nome: Tiago Matta Machado Zaidan
  //   Matricula: 451620
  //   000 - not em x
  //   001 - or
  //   010 - nor
  //   011 - and
  //   100 - nand
  //   101 - xor
  //   110 - xnor
  //   111 - retorna 0
endmodule
