// Logisim project CircuitosGuia03.circ as structural Verilog: 7 circuits, main circuit Exemplo0032
module Exemplo0031 (
  input  [3:0] A,
  input  [3:0] B,
  output [7:0] S
);

  assign S[3:0] = A | B;  // OR_Gate or_1, 4 bits wide
  assign S[7:4] = A & B;  // AND_Gate and_1, 4 bits wide

  // Notes on the sheet:
  //   Exemplo0031
  //   Wadson Ferreira - 460631
  //   e os quatro ultimos o resultado de or(a,b)
  //   A saida é composta de 8 bits, sendo os 4 primeiros o resultado de AND(a,b)
endmodule

module Exemplo0032 (
  input  S,
  input  A,
  input  B,
  output out_4
);

  wire and_1_out, not_1_out, or_1_out;

  and and_1 (and_1_out, A, B);
  or or_1 (or_1_out, A, B);
  assign out_4 = S ? or_1_out : 1'bz;  // Controlled_Buffer controlled_buffer_1
  not not_1 (not_1_out, S);
  assign out_4 = not_1_out ? and_1_out : 1'bz;  // Controlled_Buffer controlled_buffer_2

  // Notes on the sheet:
  //   Exemplo0032
  //   Wadson Ferreira - 460631
endmodule

module Exemplo0033 (
  input  S,
  input  A,
  input  B,
  output [1:0] out_4
);

  wire not_1_out;
  wire [1:0] nor_1_out, or_1_out;

  and and_1 (or_1_out[1], A, B);
  or or_1 (or_1_out[0], A, B);
  nand nand_1 (nor_1_out[1], A, B);
  nor nor_1 (nor_1_out[0], A, B);
  not not_1 (not_1_out, S);
  assign out_4 = not_1_out ? or_1_out : 2'bz;  // Controlled_Buffer controlled_buffer_1
  assign out_4 = S ? nor_1_out : 2'bz;  // Controlled_Buffer controlled_buffer_2

  // Notes on the sheet:
  //   Exemplo0033
  //   Wadson Ferreira - 460631
  //   s=0 -> saida=and(a,b) or(a,b)
  //   s=1 -> saida=nand(a,b) nor(a,b)
endmodule

module Exemplo0034 (
  input  [1:0] _11___xnor_a_b,
  input  in_2,
  input  in_3,
  output out_4
);

  wire and_1_out, and_2_out, and_3_out, and_4_out, nor_1_out, not_1_out, not_2_out, or_1_out, xnor_1_out,
       xor_1_out;

  or or_1 (or_1_out, in_2, in_3);
  nor nor_1 (nor_1_out, in_2, in_3);
  xor xor_1 (xor_1_out, in_2, in_3);
  xnor xnor_1 (xnor_1_out, in_2, in_3);
  not not_1 (not_1_out, _11___xnor_a_b[1]);
  not not_2 (not_2_out, _11___xnor_a_b[0]);
  and and_1 (and_1_out, not_1_out, not_2_out);
  assign out_4 = and_1_out ? or_1_out : 1'bz;  // Controlled_Buffer controlled_buffer_1
  and and_2 (and_2_out, _11___xnor_a_b[1], not_2_out);
  and and_3 (and_3_out, not_1_out, _11___xnor_a_b[0]);
  assign out_4 = and_3_out ? nor_1_out : 1'bz;  // Controlled_Buffer controlled_buffer_2
  assign out_4 = and_2_out ? xor_1_out : 1'bz;  // Controlled_Buffer controlled_buffer_3
  and and_4 (and_4_out, _11___xnor_a_b[1], _11___xnor_a_b[0]);
  assign out_4 = and_4_out ? xnor_1_out : 1'bz;  // Controlled_Buffer controlled_buffer_4

  // Notes on the sheet:
  //   Exemplo0034
  //   Wadson Ferreira - 460631
  //   00 - or(a,b)
  //   01 - nor(a,b)
  //   10 - xor(a,b)
endmodule

module Exemplo0035 (
  input  [2:0] S,
  input  A,
  input  B,
  output out_4
);

  wire and_1_out, and_2_out, and_3_out, and_4_out, and_5_out, and_6_out, and_7_out, and_8_out, nand_1_out,
       nor_1_out, not_1_out, not_2_out, not_3_out, not_4_out, or_1_out, xnor_1_out, xor_1_out;

  not not_1 (not_1_out, S[2]);
  not not_2 (not_2_out, S[1]);
  not not_3 (not_3_out, S[0]);
  not not_4 (not_4_out, A);
  or or_1 (or_1_out, A, B);
  nor nor_1 (nor_1_out, A, B);
  and and_1 (and_1_out, A, B);
  nand nand_1 (nand_1_out, A, B);
  xor xor_1 (xor_1_out, A, B);
  xnor xnor_1 (xnor_1_out, A, B);
  and and_2 (and_2_out, not_1_out, not_2_out, not_3_out);
  and and_3 (and_3_out, not_1_out, not_2_out, S[0]);
  assign out_4 = and_2_out ? not_4_out : 1'bz;  // Controlled_Buffer controlled_buffer_1
  assign out_4 = and_3_out ? or_1_out : 1'bz;  // Controlled_Buffer controlled_buffer_2
  and and_4 (and_4_out, not_1_out, S[1], not_3_out);
  and and_5 (and_5_out, not_1_out, S[1], S[0]);
  assign out_4 = and_4_out ? nor_1_out : 1'bz;  // Controlled_Buffer controlled_buffer_3
  assign out_4 = and_5_out ? and_1_out : 1'bz;  // Controlled_Buffer controlled_buffer_4
  and and_6 (and_6_out, S[2], not_2_out, S[0]);
  and and_7 (and_7_out, S[2], not_2_out, not_3_out);
  assign out_4 = and_7_out ? nand_1_out : 1'bz;  // Controlled_Buffer controlled_buffer_5
  assign out_4 = and_6_out ? xor_1_out : 1'bz;  // Controlled_Buffer controlled_buffer_6
  and and_8 (and_8_out, S[2], S[1], not_3_out);
  assign out_4 = and_8_out ? xnor_1_out : 1'bz;  // Controlled_Buffer controlled_buffer_7

  // Notes on the sheet:
  //   Exemplo0034
  //   Wadson Ferreira - 460631
  //   000 - not(a)
  //   001 - or(a,b)
  //   010 - nor(a,b)
  //   011 - and(a,b)
  //   100 - nand(a,b)
  //   101 - xor(a,b)
  //   110 - xnor(a,b)
endmodule

module Exemplo0036 (
  input  in_1,
  input  [1:0] in_2,
  input  [1:0] in_3,
  output out_4
);

  wire and_1_out, and_2_out, not_1_out, not_2_out, not_3_out, not_4_out, not_5_out, or_1_out, xnor_1_out;

  not not_1 (not_1_out, in_2[1]);
  not not_2 (not_2_out, in_2[0]);
  not not_3 (not_3_out, in_3[1]);
  not not_4 (not_4_out, in_3[0]);
  and and_1 (and_1_out, not_1_out, in_2[0], not_3_out, in_3[0]);
  and and_2 (and_2_out, in_2[1], not_2_out, in_3[1], not_4_out);
  NotExactlyOne xnor_1 (.out(xnor_1_out), .in0(in_2[1]), .in1(in_2[0]), .in2(in_3[1]), .in3(in_3[0]));
  or or_1 (or_1_out, xnor_1_out, and_1_out, and_2_out);
  not not_5 (not_5_out, in_1);
  assign out_4 = in_1 ? or_1_out : 1'bz;  // Controlled_Buffer controlled_buffer_1
  assign out_4 = not_5_out ? or_1_out : 1'bz;  // Controlled_Buffer controlled_buffer_2

  // Notes on the sheet:
  //   Exemplo0036
  //   Wadson Ferreira - 460631
  //   s=0 -> 
  //   s=1 -> saida=nand(a,b) nor(a,b)
endmodule

module Exemplo0037 (
  input  chave,
  input  a,
  input  b,
  input  c,
  input  d,
  output s
);

  wire and_1_out, and_2_out, and_3_out, and_4_out, and_5_out, and_6_out, not_1_out, not_2_out, not_3_out,
       not_4_out, or_1_out;

  not not_1 (not_1_out, c);
  not not_2 (not_2_out, d);
  and and_1 (and_1_out, b, not_1_out, not_2_out);
  and and_2 (and_2_out, a, not_1_out, not_2_out);
  and and_3 (and_3_out, a, not_1_out, d);
  and and_4 (and_4_out, a, b, c, not_2_out);
  not not_3 (not_3_out, chave);
  not not_4 (not_4_out, or_1_out);
  or or_1 (or_1_out, and_1_out, and_2_out, and_3_out, and_4_out);
  and and_5 (and_5_out, not_3_out, or_1_out);
  and and_6 (and_6_out, chave, not_4_out);
  or or_2 (s, and_5_out, and_6_out);

  // Notes on the sheet:
  //   Exemplo0037
  //   Wadson Ferreira - 460631
  //   chave=0  operandoA>operandoB
  //   chave=1  operandoA<=operandoB
endmodule
