// Logisim project Exercicio0011.circ as structural Verilog: 1 circuit, main circuit main
module main (
  input  A,
  input  B,
  input  C,
  input  D,
  input  E,
  input  F,
  input  G,
  input  H,
  output out_9
);

  wire or_1_out, or_2_out;

  or or_1 (or_1_out, A, B, C, D);
  or or_2 (or_2_out, E, F, G, H);
  nor nor_1 (out_9, or_1_out, or_2_out);

  // Notes on the sheet:
  //   S1
  //   S2
  //   Exercício0011 - EXTRA
  //   João Henrique Mendes de Oliveira - 392734
  //   S
endmodule
