// Logisim project Exercicio0012.circ as structural Verilog: 1 circuit, main circuit main
module main (
  input  A,
  input  B,
  input  C,
  input  D,
  input  E,
  input  F,
  input  G,
  input  H,
  output S
);

  wire or_1_out, or_2_out;

  or or_1 (or_1_out, A, B, C, D);
  or or_2 (or_2_out, E, F, G, H);
  or or_3 (S, or_1_out, or_2_out);

  // Notes on the sheet:
  //   S1
  //   S2
  //   Exercício0012 - EXTRA
  //   João Henrique Mendes de Oliveira - 392734
endmodule
