// Logisim project Exercicio0016.circ as structural Verilog: 1 circuit, main circuit Questão 11
module \Questão_11  (
  input  [7:0] A,
  output out_2
);

  nor nor_1 (out_2, A[0], A[1], A[2], A[3], A[4], A[5], A[6], A[7]);
endmodule
