// Logisim project Exercicio0017.circ as structural Verilog: 1 circuit, main circuit Questão 12
module \Questão_12  (
  input  [7:0] B,
  output out_2
);

  or or_1 (out_2, B[0], B[1], B[2], B[3], B[4], B[5], B[6], B[7]);
endmodule
