// Logisim project Questão Extra - 06 - Circuito Complemento de Um.circ as structural Verilog: 1 circuit, main circuit main
module main (
  input  [7:0] in_1,
  output [7:0] out_2
);

  assign out_2 = ~in_1;  // NOT_Gate not_1, 8 bits wide

  // Notes on the sheet:
  //   Matricula : 449517
  //   Ana Carolina Conceição de Jesus
  //   Exercicio Extra  ED 02 - 06 - Complemeto de 1 para um byte
endmodule
