// Logisim project Exercicio0007 - Complemento de 2.circ as structural Verilog: 2 circuits, main circuit Complemento de 1
module Complemento_de_1 (
  input  [7:0] in_1,
  output [7:0] out_2
);

  assign out_2 = ~in_1;  // NOT_Gate not_1, 8 bits wide

  // Notes on the sheet:
  //   Guia 02 - Exercicio0007 - Extras
  //   João Henrique - 392734
endmodule

module Complemento_de_2 (
  input  [7:0] Input____1_byte,
  output [7:0] Output
);

  wire [7:0] complemento_de_1_1_out_2;

  Complemento_de_1 complemento_de_1_1 (.in_1(Input____1_byte), .out_2(complemento_de_1_1_out_2));
  // Probe on {8{1'b0}}
  Adder adder_1 (.a(complemento_de_1_1_out_2), .b({8{1'b0}}), .out(Output), .cin(1'b1));  // open: cout

  // Notes on the sheet:
  //   Complemento de 1
  //   Guia 02 - Exercicio0007 - Extras
  //   João Henrique - 392734
endmodule
