// Logisim project complement2_1byte.circ as structural Verilog: 4 circuits, main circuit main
// c2
module complemento (
  input  [7:0] \input ,
  output OverFlow,
  output [7:0] \output 
);

  wire fulladder_2_carryout, fulladder_3_carryout, fulladder_4_carryout, fulladder_5_carryout,
       fulladder_6_carryout, fulladder_7_carryout, fulladder_8_carryout;
  wire [7:0] not_1_out;

  FullAdder fulladder_1 (
    .CarryOut(OverFlow), .CarryIn(fulladder_2_carryout), .a(not_1_out[7]), .b(1'b0), .s0(\output [7]));
  FullAdder fulladder_2 (
    .CarryOut(fulladder_2_carryout), .CarryIn(fulladder_4_carryout), .a(not_1_out[6]), .b(1'b0),
    .s0(\output [6]));
  FullAdder fulladder_3 (
    .CarryOut(fulladder_3_carryout), .CarryIn(fulladder_5_carryout), .a(not_1_out[4]), .b(1'b0),
    .s0(\output [4]));
  FullAdder fulladder_4 (
    .CarryOut(fulladder_4_carryout), .CarryIn(fulladder_3_carryout), .a(not_1_out[5]), .b(1'b0),
    .s0(\output [5]));
  FullAdder fulladder_5 (
    .CarryOut(fulladder_5_carryout), .CarryIn(fulladder_6_carryout), .a(not_1_out[3]), .b(1'b0),
    .s0(\output [3]));
  FullAdder fulladder_6 (
    .CarryOut(fulladder_6_carryout), .CarryIn(fulladder_8_carryout), .a(not_1_out[2]), .b(1'b0),
    .s0(\output [2]));
  FullAdder fulladder_7 (.CarryOut(fulladder_7_carryout), .CarryIn(1'b0), .a(not_1_out[0]), .b(1'b1), .s0(\output [0]));
  FullAdder fulladder_8 (
    .CarryOut(fulladder_8_carryout), .CarryIn(fulladder_7_carryout), .a(not_1_out[1]), .b(1'b0),
    .s0(\output [1]));
  assign not_1_out = ~\input ;  // NOT_Gate not_1, 8 bits wide
endmodule

// FA
module FullAdder (
  input  a,
  input  b,
  input  CarryIn,
  output CarryOut,
  output s0
);

  wire halfadder_1_s1, halfadder_2_s0, halfadder_2_s1;

  or or_1 (CarryOut, halfadder_1_s1, halfadder_2_s1);
  halfAdder halfadder_1 (.s0(s0), .s1(halfadder_1_s1), .a(CarryIn), .b(halfadder_2_s0));
  halfAdder halfadder_2 (.s0(halfadder_2_s0), .s1(halfadder_2_s1), .a(a), .b(b));
endmodule

module main (
  input  [7:0] in_1,
  output Vai_Um_Adicional,
  output [7:0] complemento_de_2
);

  complemento complemento_1 (.OverFlow(Vai_Um_Adicional), .\input (in_1), .\output (complemento_de_2));
endmodule

// ha
module halfAdder (
  input  a,
  input  b,
  output s0,
  output s1
);

  xor xor_1 (s0, b, a);
  and and_1 (s1, a, b);
endmodule
