// Logisim project Extras0001_0002.circ as structural Verilog: 4 circuits, main circuit Extra0001
module Extra0001 (
  input  [7:0] p,
  output [7:0] s1
);

  assign s1 = ~p;  // NOT_Gate not_1, 8 bits wide

  // Notes on the sheet:
  //   Extra0001, Guia02
  //   Complemento de 1
  //   Ana Cristina - 427385
endmodule

module Extra0002 (
  input  [7:0] carry_in,
  input  [7:0] p,
  output [7:0] s1,
  output [7:0] carry_out
);

  wire [7:0] C1_s1;

  Extra0001 C1 (.p(p), .s1(C1_s1));
  Somador_Completo Somador_Completo (.carry_in(carry_in), .a(C1_s1), .b(8'h1), .carry_out(carry_out), .s(s1));

  // Notes on the sheet:
  //   Extra0002, Guia02
  //   Complemento de 2
  //   Ana Cristina - 427385
endmodule

module Meia_Soma (
  input  [7:0] a,
  input  [7:0] b,
  output [7:0] s,
  output [7:0] carry_out
);

  assign s = b ^ a;  // XOR_Gate xor, 8 bits wide
  assign carry_out = b & a;  // AND_Gate and, 8 bits wide

  // Notes on the sheet:
  //   Meia soma
endmodule

module Somador_Completo (
  input  [7:0] carry_in,
  input  [7:0] a,
  input  [7:0] b,
  output [7:0] s,
  output [7:0] carry_out
);

  wire [7:0] Meia_Soma_2_carry_out, Meia_Soma_carry_out, Meia_Soma_s;

  Meia_Soma Meia_Soma (.a(a), .b(b), .s(Meia_Soma_s), .carry_out(Meia_Soma_carry_out));
  assign carry_out = Meia_Soma_carry_out | Meia_Soma_2_carry_out;  // OR_Gate or_1, 8 bits wide
  Meia_Soma Meia_Soma_2 (.a(Meia_Soma_s), .b(carry_in), .s(s), .carry_out(Meia_Soma_2_carry_out));

  // Notes on the sheet:
  //   Somador Completo
endmodule
