// Logisim project Questão Extra - 07 - Ed02 - Circuito Complemento de 2.circ as structural Verilog: 1 circuit, main circuit main
module main (
  input  in_1,
  input  [7:0] in_2,
  input  [7:0] in_3,
  output [7:0] out_4,
  output out_5
);

  wire [7:0] not_1_out;

  assign not_1_out = ~in_2;  // NOT_Gate not_1, 8 bits wide
  Adder adder_1 (.a(not_1_out), .b(in_3), .out(out_4), .cin(in_1), .cout(out_5));

  // Notes on the sheet:
  //   Matricula : 449517
  //   Exercicio Extra - ED 02 - Complemento de 2
  //   Ana Carolina Conceição de Jesus
endmodule
