// Logisim project guia0032.circ as structural Verilog: 1 circuit, main circuit main
module main (
  input  a,
  input  b,
  input  selecionar,
  output out_4,
  output out_5
);

  wire and_1_out, not_1_out, or_1_out;

  and and_1 (and_1_out, a, b);
  or or_1 (or_1_out, a, b);
  and p__and (out_4, selecionar, and_1_out);
  not not_1 (not_1_out, selecionar);
  and p__or (out_5, not_1_out, or_1_out);
endmodule
