// Logisim project guia0033.circ as structural Verilog: 1 circuit, main circuit main
module main (
  input  a,
  input  b,
  input  in_3,
  output out_4,
  output out_5,
  output out_6,
  output out_7
);

  wire and_1_out, nand_1_out, nor_1_out, not_1_out, or_1_out;

  nand nand_1 (nand_1_out, a, b, b);
  nor nor_1 (nor_1_out, a, b);
  and and_1 (and_1_out, a, b);
  or or_1 (or_1_out, a, b);
  not not_1 (not_1_out, in_3);
  and and_2 (out_4, nand_1_out, in_3);
  and and_3 (out_5, nor_1_out, in_3);
  and and_4 (out_6, not_1_out, and_1_out);
  and and_5 (out_7, not_1_out, or_1_out);
endmodule
