// Logisim project guia0034.circ as structural Verilog: 1 circuit, main circuit main
module main (
  input  in_1,
  input  in_2,
  input  in_3,
  input  in_4,
  output out_5,
  output out_6,
  output out_7,
  output out_8
);

  wire nor_1_out, not_1_out, not_2_out, or_1_out, xnor_1_out, xor_1_out;

  xor xor_1 (xor_1_out, in_1, in_2);
  xnor xnor_1 (xnor_1_out, in_1, in_2);
  or or_1 (or_1_out, in_1, in_2);
  nor nor_1 (nor_1_out, in_2, in_2);
  not not_1 (not_1_out, in_3);
  not not_2 (not_2_out, in_4);
  and and_1 (out_5, in_3, not_2_out, xor_1_out);
  and and_2 (out_6, in_3, in_4, xnor_1_out);
  and and_3 (out_7, not_1_out, or_1_out, not_2_out);
  and and_4 (out_8, not_1_out, in_4, nor_1_out);
endmodule
