// Logisim project guia0035.circ as structural Verilog: 1 circuit, main circuit main
module main (
  input  a,
  input  b,
  input  [2:0] c,
  output out_4,
  output out_5,
  output out_6,
  output out_7,
  output out_8,
  output out_9,
  output out_10
);

  wire and_1_out, nand_1_out, nor_1_out, not_1_out, not_2_out, not_3_out, not_4_out, or_1_out, xnor_1_out,
       xor_1_out;

  and and_1 (and_1_out, a, b);
  nand nand_1 (nand_1_out, a, b);
  or or_1 (or_1_out, a, b);
  nor nor_1 (nor_1_out, a, b);
  xor xor_1 (xor_1_out, a, b);
  xnor xnor_1 (xnor_1_out, a, b);
  not not_1 (not_1_out, b);
  not not_2 (not_2_out, c[2]);
  not not_3 (not_3_out, c[0]);
  not not_4 (not_4_out, c[1]);
  and p__and (out_4, not_2_out, not_4_out, and_1_out, not_3_out);
  and p__nand (out_5, not_2_out, not_4_out, nand_1_out, c[0]);
  and p__or (out_6, not_2_out, c[1], or_1_out, not_3_out);
  and p__nor (out_7, not_2_out, c[1], nor_1_out, c[0]);
  and p__xor (out_8, c[2], not_4_out, xor_1_out, not_3_out);
  and p__xnor (out_9, c[2], not_4_out, xnor_1_out, c[0]);
  and p__not (out_10, c[2], not_1_out, c[1], not_3_out);
endmodule
