// Logisim project Exemplo0035.circ as structural Verilog: 1 circuit, main circuit main
module main (
  input  in_1,
  input  in_2,
  output out_3,
  output out_4,
  output out_5,
  output out_6,
  output out_7,
  output out_8,
  output out_9,
  output out_10
);

  not not_1 (out_3, in_2);
  not not_2 (out_4, in_1);
  and and_1 (out_5, in_2, in_1);
  or or_1 (out_6, in_2, in_1);
  nand nand_1 (out_7, in_2, in_1);
  nor nor_1 (out_8, in_2, in_1);
  xor xor_1 (out_9, in_2, in_1);
  xnor xnor_1 (out_10, in_2, in_1);

  // Notes on the sheet:
  //   Guia 03 - Exemplo0035
  //   João Henrique Mendes de Oliveira - 392734
endmodule
