// Logisim project Guia_03_Circuitos_427385_AnaCristina.circ as structural Verilog: 10 circuits, main circuit Exemplo0031
module Exemplo0031 (
  input  [3:0] a,
  input  [3:0] b,
  output [3:0] s,
  output [3:0] s1
);

  assign s = b & a;  // AND_Gate AND, 4 bits wide
  assign s1 = b | a;  // OR_Gate OR, 4 bits wide

  // Notes on the sheet:
  //   Exemplo0031
endmodule

module Exemplo0032 (
  input  a,
  input  b,
  input  ch,
  output s
);

  wire AND_out, OR_out;

  and AND (AND_out, a, b);
  or OR (OR_out, a, b);
  Multiplexador multiplexador_1 (.a(AND_out), .b(OR_out), .ch(ch), .s(s));

  // Notes on the sheet:
  //   Ana - 427385
  //   0 - or e 1-and
  //   Exemplo0032
endmodule

// MU
module Multiplexador (
  input  a,
  input  b,
  input  ch,
  output s
);

  wire and_1_out, and_2_out, not_1_out;

  and and_1 (and_1_out, a, ch);
  and and_2 (and_2_out, b, not_1_out);
  not not_1 (not_1_out, ch);
  or or_1 (s, and_1_out, and_2_out);

  // Notes on the sheet:
  //   Multiplexador
endmodule

module Exemplo0033 (
  input  a,
  input  b,
  input  ch,
  output s0,
  output s1
);

  wire AND_out, NAND_out, NOR_out, OR_out;

  and AND (AND_out, a, b);
  or OR (OR_out, a, b);
  nand NAND (NAND_out, a, b);
  nor NOR (NOR_out, a, b);
  Multiplexador multiplexador_1 (.a(AND_out), .b(OR_out), .ch(ch), .s(s0));
  Multiplexador multiplexador_2 (.a(NAND_out), .b(NOR_out), .ch(ch), .s(s1));

  // Notes on the sheet:
  //   Ana - 427385
  //   Exemplo0033
endmodule

module Exemplo0034 (
  input  a,
  input  b,
  input  ch0,
  input  ch1,
  output s
);

  wire multiplexador_1_s, multiplexador_2_s, NOR_out, OR_out, XNOR_out, XOR_out;

  or OR (OR_out, a, b);
  xor XOR (XOR_out, a, b);
  nor NOR (NOR_out, a, b);
  xnor XNOR (XNOR_out, a, b);
  Multiplexador multiplexador_1 (.a(OR_out), .b(XOR_out), .ch(ch0), .s(multiplexador_1_s));
  Multiplexador multiplexador_2 (.a(NOR_out), .b(XNOR_out), .ch(ch0), .s(multiplexador_2_s));
  Multiplexador multiplexador_3 (.a(multiplexador_1_s), .b(multiplexador_2_s), .ch(ch1), .s(s));

  // Notes on the sheet:
  //   Ana - 427385
  //   Exemplo0034
endmodule

module Exemplo0035 (
  input  a,
  input  b,
  input  [2:0] ch,
  output s
);

  wire and_1_out, nand_1_out, nor_1_out, not_1_out, not_2_out, or_1_out, xnor_1_out, xor_1_out;

  not not_1 (not_1_out, a);
  not not_2 (not_2_out, b);
  or or_1 (or_1_out, a, b);
  nor nor_1 (nor_1_out, a, b);
  and and_1 (and_1_out, a, b);
  nand nand_1 (nand_1_out, a, b);
  xor xor_1 (xor_1_out, a, b);
  xnor xnor_1 (xnor_1_out, a, b);
  Selecionador SEL (
    .a(not_1_out), .b(not_2_out), .c(or_1_out), .d(nor_1_out), .e(and_1_out), .f(nand_1_out), .g(xor_1_out),
    .h(xnor_1_out), .ch(ch), .s(s));

  // Notes on the sheet:
  //   Exemplo0035
  //   Ana - 427385
  //   000 - NOT a
  //   001 - NOT b
  //   010 - OR
  //   011 - NOR
  //   100 - AND
  //   101 - NAND
  //   110 - XOR
  //   111 - XNOR
endmodule

// SEL
module Selecionador (
  input  a,
  input  b,
  input  c,
  input  d,
  input  e,
  input  f,
  input  g,
  input  h,
  input  [2:0] ch,
  output s
);

  wire AND_2_out, AND_3_out, AND_4_out, AND_5_out, AND_6_out, AND_7_out, AND_8_out, AND_out, not_1_out,
       not_2_out, not_3_out, not_4_out, not_5_out, not_6_out, not_7_out, not_8_out, not_9_out, not_10_out,
       not_11_out, not_12_out;

  not not_1 (not_1_out, ch[2]);
  not not_2 (not_2_out, ch[1]);
  not not_3 (not_3_out, ch[0]);
  not not_4 (not_4_out, ch[2]);
  not not_5 (not_5_out, ch[1]);
  not not_6 (not_6_out, ch[2]);
  not not_7 (not_7_out, ch[0]);
  not not_8 (not_8_out, ch[2]);
  not not_9 (not_9_out, ch[1]);
  not not_10 (not_10_out, ch[0]);
  not not_11 (not_11_out, ch[1]);
  not not_12 (not_12_out, ch[0]);
  and AND (AND_out, a, not_1_out, not_2_out, not_3_out);
  and AND_2 (AND_2_out, b, not_4_out, not_5_out, ch[0]);
  and AND_3 (AND_3_out, c, not_6_out, ch[1], not_7_out);
  and AND_4 (AND_4_out, d, not_8_out, ch[1], ch[0]);
  and AND_5 (AND_5_out, e, ch[2], not_9_out, not_10_out);
  and AND_6 (AND_6_out, f, not_11_out, ch[0]);
  and AND_7 (AND_7_out, g, ch[2], ch[1], not_12_out);
  and AND_8 (AND_8_out, h, ch[2], ch[1], ch[0]);
  or OR (s, AND_out, AND_2_out, AND_3_out, AND_4_out, AND_5_out, AND_6_out, AND_7_out, AND_8_out);
endmodule

module Exemplo0036 (
  input  [1:0] a,
  input  [1:0] b,
  input  ch,
  output [1:0] s
);

  wire [1:0] XNOR_out, XOR_out;

  assign XOR_out = a ^ b;  // XOR_Gate XOR, 2 bits wide
  assign XNOR_out = ~(b ^ a);  // XNOR_Gate XNOR, 2 bits wide
  Multiplexador_1 multiplexador_1_1 (.a(XOR_out), .b(XNOR_out), .ch({2{ch}}), .s(s));

  // Notes on the sheet:
  //   Exemplo0036
  //   Ana - 427385
  //   0 - igualdade
  //   1 - diferença
endmodule

module Exemplo0037 (
  input  [1:0] a,
  input  [1:0] b,
  output [1:0] a___b,
  output [1:0] a____b,
  output [1:0] a___b_2
);

  wire [1:0] not_1_out, not_2_out;

  assign not_1_out = ~a;  // NOT_Gate not_1, 2 bits wide
  assign a___b = not_1_out & b;  // AND_Gate and_1, 2 bits wide
  assign a___b_2 = a & not_2_out;  // AND_Gate and_2, 2 bits wide
  assign not_2_out = ~b;  // NOT_Gate not_2, 2 bits wide
  assign a____b = ~(a___b | a___b_2);  // NOR_Gate nor_1, 2 bits wide

  // Notes on the sheet:
  //   Exemplo0037
endmodule

module Multiplexador_1 (
  input  [1:0] a,
  input  [1:0] b,
  input  [1:0] ch,
  output [1:0] s
);

  wire [1:0] and_1_out, and_2_out, not_1_out;

  assign and_1_out = a & ch;  // AND_Gate and_1, 2 bits wide
  assign and_2_out = b & not_1_out;  // AND_Gate and_2, 2 bits wide
  assign not_1_out = ~ch;  // NOT_Gate not_1, 2 bits wide
  assign s = and_1_out | and_2_out;  // OR_Gate or_1, 2 bits wide

  // Notes on the sheet:
  //   Multiplexador 1
endmodule
