// Logisim project Guia03.circ as structural Verilog: 6 circuits, main circuit Exercicio0033
module Exercicio0033 (
  input  A,
  input  B,
  input  CHAVE_1,
  output out_4,
  output out_5
);

  wire and_1_out, and_2_out, and_3_out, and_4_out, and_5_out, nand_1_out, nor_1_out, not_1_out, not_2_out,
       or_1_out;

  and and_1 (and_1_out, A, B);
  nand nand_1 (nand_1_out, B, A);
  or or_1 (or_1_out, A, B);
  nor nor_1 (nor_1_out, A, B);
  not not_1 (not_1_out, CHAVE_1);
  not not_2 (not_2_out, CHAVE_1);
  and and_2 (and_2_out, and_1_out, not_1_out);
  and and_3 (and_3_out, nand_1_out, CHAVE_1);
  and and_4 (and_4_out, or_1_out, not_2_out);
  and and_5 (and_5_out, CHAVE_1, nor_1_out);
  or or_2 (out_4, and_2_out, and_3_out);
  or or_3 (out_5, and_4_out, and_5_out);

  // Notes on the sheet:
  //   chave 1/0 NAND 1/1 AND 0/1 OR 0/0 NOR
endmodule

module Exercicio0032 (
  input  A,
  input  B,
  input  CHAVE,
  output SAIDA
);

  wire and1_out, and2_out, and3_out, not_1_out, or1_out;

  and and1 (and1_out, A, B);
  or or1 (or1_out, B, A);
  not not_1 (not_1_out, CHAVE);
  and and2 (and2_out, and1_out, CHAVE);
  and and3 (and3_out, or1_out, not_1_out);
  or or2 (SAIDA, and2_out, and3_out);

  // Notes on the sheet:
  //   wire1
  //   wire2
  //   Chave 0 porta OR/Chave 1 porta AND
  //   wire3
  //   wire4
endmodule

module Exercicio0034 (
  input  in_1,
  input  in_2,
  input  [1:0] in_3,
  output out_4
);

  wire and_1_out, and_2_out, and_3_out, and_4_out, and_5_out, and_6_out, nor_1_out, not_1_out, not_2_out,
       not_3_out, or_1_out, or_2_out, or_3_out, xnor_1_out, xor_1_out;

  or or_1 (or_1_out, in_1, in_2);
  xor xor_1 (xor_1_out, in_1, in_2);
  nor nor_1 (nor_1_out, in_1, in_2);
  xnor xnor_1 (xnor_1_out, in_1, in_2);
  not not_1 (not_1_out, in_3[0]);
  and and_1 (and_1_out, or_1_out, not_2_out);
  not not_2 (not_2_out, in_3[0]);
  and and_2 (and_2_out, xor_1_out, in_3[0]);
  and and_3 (and_3_out, nor_1_out, not_1_out);
  and and_4 (and_4_out, xnor_1_out, in_3[0]);
  or or_2 (or_2_out, and_1_out, and_2_out);
  or or_3 (or_3_out, and_3_out, and_4_out);
  and and_5 (and_5_out, or_2_out, not_3_out);
  not not_3 (not_3_out, in_3[1]);
  and and_6 (and_6_out, or_3_out, in_3[1]);
  or or_4 (out_4, and_5_out, and_6_out);

  // Notes on the sheet:
  //   00
  //   10
  //   01
  //   11
endmodule

module Exercicio0035 (
  input  in_1,
  input  in_2,
  input  [2:0] in_3,
  output out_4
);

  wire _000_out, _001_out, _010_out, _011_out, _100_out, _101_out, _110_out, and_1_out, nand_1_out,
       nor_1_out, not_1_out, not_2_out, not_3_out, not_4_out, not_5_out, not_6_out, not_7_out, not_8_out,
       not_9_out, not_10_out, not_11_out, not_12_out, not_13_out, or_1_out, xnor_1_out, xor_1_out;

  or or_1 (or_1_out, in_1, in_2);
  and and_1 (and_1_out, in_1, in_2);
  nor nor_1 (nor_1_out, in_1, in_2);
  nand nand_1 (nand_1_out, in_1, in_2);
  xor xor_1 (xor_1_out, in_1, in_2);
  xnor xnor_1 (xnor_1_out, in_1, in_2);
  not not_1 (not_1_out, in_1);
  not not_2 (not_2_out, in_3[0]);
  not not_3 (not_3_out, in_3[1]);
  not not_4 (not_4_out, in_3[2]);
  not not_5 (not_5_out, in_3[1]);
  not not_6 (not_6_out, in_3[2]);
  not not_7 (not_7_out, in_3[0]);
  not not_8 (not_8_out, in_3[2]);
  not not_9 (not_9_out, in_3[2]);
  not not_10 (not_10_out, in_3[0]);
  not not_11 (not_11_out, in_3[1]);
  not not_12 (not_12_out, in_3[1]);
  not not_13 (not_13_out, in_3[0]);
  and _000 (_000_out, not_2_out, or_1_out, not_3_out, not_4_out);
  and _001 (_001_out, in_3[0], nor_1_out, not_5_out, not_6_out);
  and _010 (_010_out, not_7_out, and_1_out, in_3[1], not_8_out);
  and _011 (_011_out, in_3[0], nand_1_out, in_3[1], not_9_out);
  and _100 (_100_out, not_10_out, xor_1_out, not_11_out, in_3[2]);
  and _101 (_101_out, in_3[0], xnor_1_out, not_12_out, in_3[2]);
  and _110 (_110_out, not_13_out, not_1_out, in_3[1], in_3[2]);
  or or_2 (out_4, _000_out, _001_out, _010_out, _011_out, _100_out, _101_out, _110_out);
endmodule

module extra01 (
  input  [1:0] in_1,
  input  [1:0] in_2,
  input  _1__Diferente,
  output out_4
);

  wire and_1_out, and_2_out, and_3_out, not_1_out, not_2_out, xnor_1_out, xnor_2_out;

  xnor xnor_1 (xnor_1_out, in_2[0], in_1[0]);
  xnor xnor_2 (xnor_2_out, in_2[1], in_1[1]);
  and and_1 (and_1_out, xnor_1_out, xnor_2_out);
  not not_1 (not_1_out, _1__Diferente);
  and and_2 (and_2_out, and_1_out, not_1_out);
  not not_2 (not_2_out, and_1_out);
  and and_3 (and_3_out, not_2_out, _1__Diferente);
  or or_1 (out_4, and_2_out, and_3_out);

  // Notes on the sheet:
  //   Circuito verifica igualdade
  //   0-Igual
endmodule

module Exercicio0031 (
  input  [3:0] in_1,
  input  [3:0] in_2,
  output [3:0] out_3,
  output [3:0] out_4
);

  assign out_3 = in_1 & in_2;  // AND_Gate and_1, 4 bits wide
  assign out_4 = in_1 | in_2;  // OR_Gate or_1, 4 bits wide
endmodule
