// Logisim project exercicio.circ as structural Verilog
module ex31 (
  input  [3:0] in_1,
  input  [3:0] in_2,
  output [3:0] out_3,
  output [3:0] out_4
);

  assign out_3 = in_1 & in_2;  // AND_Gate and_1, 4 bits wide
  assign out_4 = in_1 | in_2;  // OR_Gate or_1, 4 bits wide
endmodule

module ex32 (
  input  in_1,
  input  in_2,
  input  in_3,
  input  in_4,
  input  in_5,
  input  in_6,
  output out_7,
  output out_8
);

  wire and_1_out, not_1_out, not_2_out, or_1_out, or_2_out, or_3_out, or_4_out, or_5_out;

  not not_1 (not_1_out, in_1);
  or or_1 (or_1_out, not_1_out, in_2);
  or or_2 (or_2_out, in_3, in_2);
  or or_3 (or_3_out, not_1_out, in_3);
  not not_2 (not_2_out, in_4);
  and and_1 (and_1_out, in_6, in_4, in_5);
  and and_2 (out_7, or_1_out, or_2_out, or_3_out);
  or or_4 (or_4_out, in_6, and_1_out, in_5);
  or or_5 (or_5_out, not_2_out, and_1_out);
  and and_3 (out_8, or_4_out, or_5_out);
endmodule

module ex33 (
  input  in_1,
  input  in_2,
  input  in_3,
  output out_4
);

  wire and_1_out, and_2_out, and_3_out, and_4_out, not_1_out, not_2_out, not_3_out, or_1_out, or_2_out;

  not not_1 (not_1_out, in_1);
  and and_1 (and_1_out, in_3, in_1, in_2);
  or or_1 (or_1_out, in_3, and_1_out, in_2);
  or or_2 (or_2_out, not_1_out, and_1_out);
  and and_2 (and_2_out, or_1_out, or_2_out);
  not not_2 (not_2_out, in_1);
  not not_3 (not_3_out, and_2_out);
  and and_3 (and_3_out, and_2_out, not_2_out);
  and and_4 (and_4_out, in_1, not_3_out);
  or or_3 (out_4, and_3_out, and_4_out);
endmodule

module ex34 (
  input  in_1,
  input  in_2,
  input  in_3,
  input  in_4,
  output out_5
);

  wire and_1_out, and_2_out, and_3_out, and_4_out, and_5_out, and_6_out, and_7_out, not_1_out, not_2_out,
       not_3_out, not_4_out, not_5_out, not_6_out, or_1_out, or_2_out, or_3_out, or_4_out, or_5_out;

  not not_1 (not_1_out, in_2);
  not not_2 (not_2_out, in_3);
  not not_3 (not_3_out, in_4);
  or or_1 (or_1_out, in_4, in_2, in_3);
  and and_1 (and_1_out, in_4, not_2_out);
  and and_2 (and_2_out, not_3_out, in_3);
  or or_2 (or_2_out, in_4, or_1_out, in_3);
  and and_3 (and_3_out, or_2_out, or_3_out);
  or or_3 (or_3_out, not_1_out, or_1_out);
  or or_4 (or_4_out, and_1_out, and_2_out);
  not not_4 (not_4_out, in_2);
  not not_5 (not_5_out, or_4_out);
  and and_4 (and_4_out, or_4_out, not_4_out);
  and and_5 (and_5_out, in_2, not_5_out);
  or or_5 (or_5_out, and_4_out, and_5_out);
  and and_6 (and_6_out, and_3_out, not_6_out);
  not not_6 (not_6_out, in_1);
  and and_7 (and_7_out, in_1, or_5_out);
  or or_6 (out_5, and_6_out, and_7_out);
endmodule

module ex35 (
  input  [2:0] in_1,
  input  in_2,
  input  in_3,
  output out_4
);

  wire and_1_out, and_2_out, and_3_out, and_4_out, and_5_out, and_6_out, and_7_out, and_8_out, and_9_out,
       and_10_out, and_11_out, and_12_out, and_13_out, and_14_out, not_1_out, not_2_out, not_3_out,
       not_4_out, not_5_out, not_6_out, not_7_out, not_8_out, not_9_out, or_1_out, or_2_out, or_3_out,
       or_4_out, or_5_out, or_6_out, or_7_out;

  not not_1 (not_1_out, in_1[1]);
  not not_2 (not_2_out, in_1[2]);
  not not_3 (not_3_out, in_1[0]);
  and and_1 (and_1_out, in_3, in_1[0], in_2);
  not not_4 (not_4_out, in_2);
  not not_5 (not_5_out, in_3);
  not not_6 (not_6_out, in_3);
  not not_7 (not_7_out, in_2);
  or or_1 (or_1_out, in_3, and_1_out, in_2);
  or or_2 (or_2_out, not_3_out, and_1_out);
  and and_2 (and_2_out, in_3, not_4_out);
  and and_3 (and_3_out, not_5_out, in_2);
  and and_4 (and_4_out, not_6_out, not_3_out);
  and and_5 (and_5_out, in_1[0], not_7_out);
  and and_6 (and_6_out, or_1_out, or_2_out);
  or or_3 (or_3_out, and_2_out, and_3_out);
  or or_4 (or_4_out, and_4_out, and_5_out);
  not not_8 (not_8_out, and_6_out);
  and and_7 (and_7_out, or_3_out, not_3_out);
  and and_8 (and_8_out, in_1[0], not_9_out);
  not not_9 (not_9_out, or_3_out);
  and and_9 (and_9_out, in_1[1], or_4_out);
  and and_10 (and_10_out, and_6_out, not_1_out);
  or or_5 (or_5_out, and_10_out, and_11_out);
  and and_11 (and_11_out, in_1[1], not_8_out);
  or or_6 (or_6_out, and_7_out, and_8_out);
  and and_12 (and_12_out, or_6_out, not_1_out);
  or or_7 (or_7_out, and_12_out, and_9_out);
  and and_13 (and_13_out, or_5_out, not_2_out);
  or or_8 (out_4, and_13_out, and_14_out);
  and and_14 (and_14_out, in_1[2], or_7_out);
endmodule

module ex36 (
  input  in_1,
  input  in_2,
  input  in_3,
  output out_4
);

  wire and_1_out, and_2_out, not_1_out, xnor_1_out, xor_1_out;

  not not_1 (not_1_out, in_1);
  xor xor_1 (xor_1_out, in_3, in_2);
  xnor xnor_1 (xnor_1_out, in_3, in_2);
  and and_1 (and_1_out, xor_1_out, not_1_out);
  and and_2 (and_2_out, in_1, xnor_1_out);
  or or_1 (out_4, and_1_out, and_2_out);
endmodule

module ex37 (
  input  in_1,
  input  in_2,
  input  in_3,
  input  in_4,
  input  in_5,
  input  in_6,
  input  in_7,
  input  in_8,
  input  in_9,
  input  in_10,
  output out_11,
  output out_12,
  output out_13,
  output out_14,
  output out_15
);

  wire and_1_out, and_2_out, and_4_out, and_5_out, and_6_out, and_8_out, not_1_out, not_2_out, not_4_out,
       not_5_out, or_1_out, or_2_out, or_3_out, or_4_out, or_6_out, or_7_out, or_8_out, or_9_out;

  not not_1 (not_1_out, in_3);
  not not_2 (not_2_out, in_4);
  and and_1 (and_1_out, in_6, not_1_out, in_5);
  and and_2 (and_2_out, in_6, in_5, in_3);
  or or_1 (or_1_out, in_6, and_1_out, in_5);
  or or_2 (or_2_out, not_2_out, and_1_out);
  or or_3 (or_3_out, in_6, and_2_out, in_5);
  or or_4 (or_4_out, in_4, and_2_out);
  and and_3 (out_12, or_3_out, or_4_out);
  and and_4 (and_4_out, or_1_out, or_2_out);
  not not_3 (out_14, and_4_out);
  or or_5 (out_13, out_12, in_6, in_5, out_14);
  not not_4 (not_4_out, in_7);
  and and_5 (and_5_out, in_2, in_7, in_1);
  or or_6 (or_6_out, in_2, and_5_out, in_1);
  or or_7 (or_7_out, not_4_out, and_5_out);
  not not_5 (not_5_out, in_10);
  and and_6 (and_6_out, in_9, in_10, in_8);
  and and_7 (out_11, or_6_out, or_7_out);
  or or_8 (or_8_out, in_9, and_6_out, in_8);
  or or_9 (or_9_out, not_5_out, and_6_out);
  and and_8 (and_8_out, or_8_out, or_9_out);
  not not_6 (out_15, and_8_out);
endmodule
