// Logisim project Exemplo0031.circ as structural Verilog: 1 circuit, main circuit Exemplo0031
module Exemplo0031 (
  input  A0,
  input  A1,
  input  A2,
  input  A3,
  input  B0,
  input  B1,
  input  B2,
  input  B3,
  output out_9,
  output out_10,
  output out_11,
  output out_12,
  output out_13,
  output out_14,
  output out_15,
  output out_16
);

  and and_1 (out_9, B0, A0);
  and and_2 (out_10, B1, A1);
  and and_3 (out_11, B2, A2);
  and and_4 (out_12, B3, A3);
  or or_1 (out_13, B0, A0);
  or or_2 (out_14, B1, A1);
  or or_3 (out_15, B2, A2);
  or or_4 (out_16, B3, A3);
endmodule
