// Logisim project Exemplo0032.circ as structural Verilog: 1 circuit, main circuit main
// Exemplo0032
module main (
  input  A,
  input  B,
  input  extra,
  output sAND,
  output sOR
);

  wire and_1_out, not_1_out, or_1_out;

  and and_1 (and_1_out, B, A);
  or or_1 (or_1_out, B, A);
  not not_1 (not_1_out, extra);
  and and_2 (sAND, and_1_out, extra);
  and and_3 (sOR, not_1_out, or_1_out);
endmodule
