// Logisim project Exemplo0034.circ as structural Verilog: 1 circuit, main circuit Exemplo0034
module Exemplo0034 (
  input  a,
  input  b,
  input  chave1,
  input  chave_2,
  output out_5,
  output out_6
);

  wire and_1_out, and_2_out, and_3_out, and_4_out, nor_1_out, not_1_out, not_2_out, not_3_out, not_4_out,
       or_1_out, xnor_1_out, xor_1_out;

  xor xor_1 (xor_1_out, a, a);
  xnor xnor_1 (xnor_1_out, a, a);
  or or_1 (or_1_out, a, a);
  nor nor_1 (nor_1_out, a, a);
  not not_1 (not_1_out, chave_2);
  not not_2 (not_2_out, chave1);
  not not_3 (not_3_out, chave_2);
  not not_4 (not_4_out, chave1);
  and and_1 (and_1_out, xor_1_out, chave1, not_1_out);
  and and_2 (and_2_out, xnor_1_out, chave1, chave_2);
  and and_3 (and_3_out, or_1_out, not_2_out, not_3_out);
  and and_4 (and_4_out, nor_1_out, not_4_out, chave_2);
  or or_2 (out_5, and_1_out, and_2_out);
  or or_3 (out_6, and_3_out, and_4_out);

  assign b = a;
endmodule
