// Logisim project Exemplo0036.circ as structural Verilog: 1 circuit, main circuit Exemplo0036
module Exemplo0036 (
  input  a,
  input  b,
  input  chave,
  output s0___chave_1,
  output s1___chave_0
);

  wire not_1_out, xnor_1_out, xor_1_out;

  xor xor_1 (xor_1_out, a, b);
  xnor xnor_1 (xnor_1_out, a, b);
  not not_1 (not_1_out, chave);
  and and_1 (s0___chave_1, xor_1_out, chave);
  and and_2 (s1___chave_0, xnor_1_out, not_1_out);
endmodule
