// Logisim project Exemplo31.circ as structural Verilog: 2 circuits, main circuit LU (AND/OR)
// LU
module LU__AND_OR (
  input  [3:0] in_1,
  input  [3:0] in_2,
  output [3:0] out_3,
  output [3:0] out_4
);

  assign out_3 = in_1 & in_2;  // AND_Gate and_1, 4 bits wide
  assign out_4 = in_1 | in_2;  // OR_Gate or_1, 4 bits wide
endmodule

module Exemplo31 (
  input  [3:0] in_1,
  input  [3:0] in_2,
  input  [3:0] in_3,
  output [3:0] out_4
);

  wire [3:0] and_1_out, and_2_out, lu_and_or_1_out_3, lu_and_or_1_out_4, not_1_out;

  LU__AND_OR lu_and_or_1 (.in_1(in_1), .in_2(in_2), .out_3(lu_and_or_1_out_3), .out_4(lu_and_or_1_out_4));
  assign not_1_out = ~in_3;  // NOT_Gate not_1, 4 bits wide
  assign and_1_out = not_1_out & lu_and_or_1_out_3;  // AND_Gate and_1, 4 bits wide
  assign and_2_out = lu_and_or_1_out_4 & in_3;  // AND_Gate and_2, 4 bits wide
  assign out_4 = and_1_out | and_2_out;  // OR_Gate or_1, 4 bits wide

  // Notes on the sheet:
  //   Exemplo 31
  //   0000 - AND
  //                 1111 - OR
endmodule
