// Logisim project Exemplo32.circ as structural Verilog: 2 circuits, main circuit Lu
// LU
module Lu (
  input  in_1,
  input  in_2,
  output out_3,
  output out_4
);

  and and_1 (out_3, in_1, in_2);
  or or_1 (out_4, in_2, in_1);
endmodule

module Exemplo32 (
  input  x,
  input  y,
  input  _0_AND,
  output out_4
);

  wire and_1_out, and_2_out, lu_1_out_3, lu_1_out_4, not_1_out;

  Lu lu_1 (.in_1(x), .in_2(y), .out_3(lu_1_out_3), .out_4(lu_1_out_4));
  not not_1 (not_1_out, _0_AND);
  and and_1 (and_1_out, not_1_out, lu_1_out_3);
  and and_2 (and_2_out, lu_1_out_4, _0_AND);
  or or_1 (out_4, and_1_out, and_2_out);

  // Notes on the sheet:
  //   Exemplo32
  //   chave
  //   1-OR
endmodule
