// Logisim project Exemplo33.circ as structural Verilog: 1 circuit, main circuit main
module main (
  input  _1__OR,
  input  in_2,
  input  in_3,
  input  in_4,
  input  in_5,
  output out_6
);

  wire and_1_out, multiplexer_1_out, multiplexer_2_out, nand_1_out, nor_1_out, or_1_out;

  and and_1 (and_1_out, in_2, in_3);
  or or_1 (or_1_out, in_2, in_3);
  nand nand_1 (nand_1_out, in_2, in_3);
  nor nor_1 (nor_1_out, in_2, in_3);
  Multiplexer #(.enable("false")) multiplexer_1 (
    .in0(and_1_out), .in1(or_1_out), .out(multiplexer_1_out), .sel(_1__OR));
  Multiplexer #(.enable("false")) multiplexer_2 (
    .in0(nand_1_out), .in1(nor_1_out), .out(multiplexer_2_out), .sel(in_5));
  Multiplexer #(.enable("false")) multiplexer_3 (
    .in0(multiplexer_1_out), .in1(multiplexer_2_out), .out(out_6), .sel(in_4));

  // Notes on the sheet:
  //   0 - NAND
  //   1 - NOR
  //   0 - AND
  //   0 - AND/OR
  //   1 - NAND/NOR
endmodule
