// Logisim project Exemplo34.circ as structural Verilog: 3 circuits, main circuit or/nor
module or_nor (
  input  in_1,
  input  in_2,
  output out_3,
  output out_4
);

  or or_1 (out_3, in_1, in_2);
  nor nor_1 (out_4, in_1, in_2);
endmodule

module xor_xnor (
  input  in_1,
  input  in_2,
  output out_3,
  output out_4
);

  xor xor_1 (out_3, in_1, in_2);
  xnor xnor_1 (out_4, in_1, in_2);
endmodule

module Exemplo34 (
  input  in_1,
  input  in_2,
  input  [1:0] in_3,
  output out_4
);

  wire and_1_out, and_2_out, and_3_out, and_4_out, not_1_out, not_2_out, or_nor_1_out_3, or_nor_1_out_4,
       xor_xnor_1_out_3, xor_xnor_1_out_4;

  or_nor or_nor_1 (.in_1(in_1), .in_2(in_2), .out_3(or_nor_1_out_3), .out_4(or_nor_1_out_4));
  xor_xnor xor_xnor_1 (.in_1(in_1), .in_2(in_2), .out_3(xor_xnor_1_out_3), .out_4(xor_xnor_1_out_4));
  not not_1 (not_1_out, in_3[1]);
  and and_1 (and_1_out, or_nor_1_out_3, not_1_out, not_2_out);
  and and_2 (and_2_out, or_nor_1_out_4, not_1_out, in_3[0]);
  and and_3 (and_3_out, xor_xnor_1_out_3, in_3[1], not_2_out);
  and and_4 (and_4_out, xor_xnor_1_out_4, in_3[1], in_3[0]);
  not not_2 (not_2_out, in_3[0]);
  or or_1 (out_4, and_1_out, and_2_out, and_3_out, and_4_out);

  // Notes on the sheet:
  //   11 - xnor
  //   00 - or
  //   01 - nor
  //   10 - xor
endmodule
