// Logisim project Exemplo36.circ as structural Verilog: 1 circuit, main circuit main
module main (
  input  a0,
  input  a1,
  input  b0,
  input  b1,
  input  in_5,
  output out_6
);

  wire or_1_out, xor_1_out, xor_2_out;

  xor xor_1 (xor_1_out, b0, b1);
  xor xor_2 (xor_2_out, a0, a1);
  or or_1 (or_1_out, xor_2_out, xor_1_out);
  xor xor_3 (out_6, or_1_out, in_5);

  // Notes on the sheet:
  //   0 - iguais
  //   1 - diferente
  //   Se sair 1 , sao diferentes
  //   Se sair 0 , são iguais
endmodule
