// Logisim project Exemplo37.circ as structural Verilog: 1 circuit, main circuit main
module main (
  input  A1,
  input  A0,
  input  B1,
  input  B0,
  output EQ_A_B,
  output GT_A_B,
  output LT_A_B
);

  wire and_2_out, and_3_out, and_4_out, and_5_out, not_1_out, not_2_out, not_3_out, not_4_out, xor_1_out,
       xor_2_out;

  not not_1 (not_1_out, A1);
  not not_2 (not_2_out, A0);
  not not_3 (not_3_out, B1);
  not not_4 (not_4_out, B0);
  xor xor_1 (xor_1_out, A1, not_3_out);
  xor xor_2 (xor_2_out, A0, not_4_out);
  and and_1 (EQ_A_B, xor_1_out, xor_2_out);
  and and_2 (and_2_out, A1, not_3_out);
  and and_3 (and_3_out, xor_1_out, A0, not_4_out);
  and and_4 (and_4_out, B1, not_1_out);
  and and_5 (and_5_out, xor_1_out, not_2_out, B0);
  or or_1 (GT_A_B, and_2_out, and_3_out);
  or or_2 (LT_A_B, and_4_out, and_5_out);
endmodule
