// Logisim project Simulacao.circ as structural Verilog
module Exemplo0031 (
  input  [3:0] in_1,
  input  [3:0] in_2,
  output [3:0] out_3,
  output [3:0] out_4
);

  assign out_3 = in_1 & in_2;  // AND_Gate and_1, 4 bits wide
  assign out_4 = in_1 | in_2;  // OR_Gate or_1, 4 bits wide
endmodule

module Exemplo0032 (
  input  _0___AND,
  input  in_2,
  input  in_3,
  output out_4
);

  wire and_1_out, and_2_out, and_3_out, or_1_out;

  and and_1 (and_1_out, in_2, _0___AND);
  and and_2 (and_2_out, _0___AND, in_3);
  and and_3 (and_3_out, in_2, in_3);
  or or_1 (or_1_out, and_1_out, and_2_out);
  or or_2 (out_4, or_1_out, and_3_out);

  // Notes on the sheet:
  //   1 - OR
endmodule

module Exemplo0033 (
  input  in_1,
  input  in_2,
  input  _0____AND_e_OR,
  output AND_e_NAND,
  output OR_e_NOR
);

  wire and_1_out, and_2_out, and_3_out, and_4_out, and_5_out, nand_1_out, nor_1_out, not_1_out, or_1_out;

  nand nand_1 (nand_1_out, in_1, in_2);
  nor nor_1 (nor_1_out, in_2, in_1);
  and and_1 (and_1_out, in_2, in_1);
  or or_1 (or_1_out, in_1, in_2);
  not not_1 (not_1_out, _0____AND_e_OR);
  and and_2 (and_2_out, nand_1_out, _0____AND_e_OR);
  and and_3 (and_3_out, _0____AND_e_OR, nor_1_out);
  and and_4 (and_4_out, and_1_out, not_1_out);
  and and_5 (and_5_out, not_1_out, or_1_out);
  or or_2 (AND_e_NAND, and_2_out, and_4_out);
  or or_3 (OR_e_NOR, and_3_out, and_5_out);

  // Notes on the sheet:
  //   1 - NAND e NOR
endmodule

module Exemplo0034 (
  input  in_1,
  input  in_2,
  input  _0____OR_e_NOR,
  output OR_e_XNOR,
  output NOR_e_XNOR
);

  wire and_1_out, and_2_out, and_3_out, and_4_out, nor_out, not_1_out, or_out, xnor_out, xor_out;

  xor \xor  (xor_out, in_1, in_2);
  or \or  (or_out, in_2, in_1);
  nor \nor  (nor_out, in_1, in_2);
  xnor \xnor  (xnor_out, in_2, in_1);
  and and_1 (and_1_out, xor_out, _0____OR_e_NOR);
  and and_2 (and_2_out, _0____OR_e_NOR, xnor_out);
  and and_3 (and_3_out, or_out, not_1_out);
  and and_4 (and_4_out, not_1_out, nor_out);
  not not_1 (not_1_out, _0____OR_e_NOR);
  or or_2 (OR_e_XNOR, and_1_out, and_3_out);
  or or_3 (NOR_e_XNOR, and_2_out, and_4_out);

  // Notes on the sheet:
  //   1 - XOR e XNOR
endmodule

module Exemplo0035 (
  input  in_1,
  input  in_2,
  input  [2:0] _010___OR,
  output out_4
);

  wire _000_out, _001_out, _010_out, _011_out, _100_out, _101_out, _110_out, _111_out, and_1_out, nand_1_out,
       nor_1_out, not_1_out, not_2_out, not_3_out, not_4_out, not_5_out, not_6_out, not_7_out, not_8_out,
       not_9_out, not_10_out, not_11_out, not_12_out, not_13_out, not_14_out, or_1_out, xnor_1_out, xor_1_out;

  not not_1 (not_1_out, in_1);
  not not_2 (not_2_out, in_2);
  or or_1 (or_1_out, in_1, in_2);
  nor nor_1 (nor_1_out, in_1, in_2);
  and and_1 (and_1_out, in_1, in_2);
  nand nand_1 (nand_1_out, in_1, in_2);
  xor xor_1 (xor_1_out, in_1, in_2);
  xnor xnor_1 (xnor_1_out, in_1, in_2);
  not not_3 (not_3_out, _010___OR[2]);
  not not_4 (not_4_out, _010___OR[1]);
  not not_5 (not_5_out, _010___OR[0]);
  not not_6 (not_6_out, _010___OR[1]);
  not not_7 (not_7_out, _010___OR[2]);
  not not_8 (not_8_out, _010___OR[2]);
  not not_9 (not_9_out, _010___OR[0]);
  not not_10 (not_10_out, _010___OR[2]);
  not not_11 (not_11_out, _010___OR[1]);
  not not_12 (not_12_out, _010___OR[0]);
  not not_13 (not_13_out, _010___OR[1]);
  not not_14 (not_14_out, _010___OR[0]);
  and _000 (_000_out, not_3_out, not_4_out, not_5_out, not_1_out);
  and _001 (_001_out, not_6_out, not_7_out, _010___OR[0], not_2_out);
  and _010 (_010_out, not_8_out, _010___OR[1], not_9_out, or_1_out);
  and _011 (_011_out, not_10_out, _010___OR[1], _010___OR[0], nor_1_out);
  and _100 (_100_out, not_11_out, not_12_out, and_1_out);
  and _101 (_101_out, _010___OR[2], not_13_out, _010___OR[0], nand_1_out);
  and _110 (_110_out, _010___OR[2], _010___OR[1], not_14_out, xor_1_out);
  and _111 (_111_out, _010___OR[2], _010___OR[1], _010___OR[0], xnor_1_out);
  or or_2 (out_4, _000_out, _001_out, _010_out, _011_out, _100_out, _101_out, _110_out, _111_out);

  // Notes on the sheet:
  //   000 - NOT
  //   001 - NOT
  //   011 - NOR
  //   100 - AND
  //   101 - NAND
  //   110 - XOR
  //   111 - XNOR
endmodule
