// Logisim project circuito Exemplo0032.circ as structural Verilog: 1 circuit, main circuit main
module main (
  input  in_1,
  input  chave,
  input  in_3,
  input  in_4,
  input  in_5,
  output out_6,
  output out_7
);

  wire and_1_out, and_2_out, and_3_out, and_4_out, not_1_out, or_1_out, or_2_out;

  and and_1 (and_1_out, in_1, chave);
  or or_1 (or_1_out, in_1, chave);
  buf and_2 (and_2_out, and_1_out);  // AND_Gate
  and and_3 (and_3_out, or_1_out, not_1_out);
  not not_1 (not_1_out, chave);
  and and_4 (and_4_out, in_3, in_4);
  Multiplexer multiplexer_1 (.in0(and_4_out), .in1(or_2_out), .out(out_7), .sel(in_5));  // open: en
  or or_2 (or_2_out, in_3, in_4);
  or or_3 (out_6, and_2_out, and_3_out);

  // Notes on the sheet:
  //   Multiplexador 
  //   com operaçoes and e or
endmodule
