// Logisim project circuito Exemplo0033.circ as structural Verilog: 1 circuit, main circuit main
module main (
  input  in_1,
  input  chave,
  output out_3
);

  wire and_1_out, and_2_out, and_3_out, nand_1_out, nor_1_out, not_1_out, or_1_out;

  buf and_1 (and_1_out, in_1);  // AND_Gate
  buf or_1 (or_1_out, in_1);  // OR_Gate
  not nor_1 (nor_1_out, in_1);  // NOR_Gate
  not nand_1 (nand_1_out, in_1);  // NAND_Gate
  and and_2 (and_2_out, and_1_out, chave, or_1_out);
  not not_1 (not_1_out, chave);
  or or_2 (out_3, and_2_out, and_3_out);
  and and_3 (and_3_out, nor_1_out, nand_1_out, not_1_out);

  // Notes on the sheet:
  //   Exemplo0033
  //   Or e and  - chave = 1
  //   Nand e Nor  - chave = 0
  //   Ana Carolina Conceição de Jesus Matricula 449517
endmodule
