// Logisim project circuito Exemplo0034.circ as structural Verilog: 1 circuit, main circuit main
module main (
  input  a,
  input  b,
  input  chave0,
  input  chave1,
  output s
);

  wire and_1_out, and_2_out, and_3_out, and_4_out, nor_1_out, not_1_out, not_2_out, or_1_out, xnor_1_out,
       xor_1_out;

  or or_1 (or_1_out, a, b);
  nor nor_1 (nor_1_out, a, b);
  xor xor_1 (xor_1_out, a, b);
  xnor xnor_1 (xnor_1_out, a, b);
  not not_1 (not_1_out, chave0);
  not not_2 (not_2_out, chave1);
  and and_1 (and_1_out, or_1_out, chave0, chave1);
  and and_2 (and_2_out, nor_1_out, chave0, not_2_out);
  and and_3 (and_3_out, xor_1_out, not_1_out, chave1);
  and and_4 (and_4_out, xnor_1_out, not_1_out, not_2_out);
  or or_2 (s, and_1_out, and_2_out, and_3_out, and_4_out);

  // Notes on the sheet:
  //   Matricula 449517
  //   Exemplo0034 - ED 03 -  Ana Carolina Conceição de Jesus
  //   s3
  //   s2
  //   s1
  //   s0
  //   tmp3
  //   tmp2
  //   tmp1
  //   tmp0
  //   Chaves 
  //   01 - XOR
  //   10 - NOR
  //   11 - OR
  //   operação
  //   00 - XNOR
endmodule
