// Logisim project circuito Exemplo0035.circ as structural Verilog: 1 circuit, main circuit main
module main (
  input  entrada,
  input  chave0,
  input  chave1,
  input  chave2,
  output saida
);

  wire _1_2_out, _1_out, _2_out, _3_out, _4_out, _5_out, _6_out, _7_out, _8_out, nand_1_out, not_1_out,
       not_2_out, not_3_out, not_4_out, or_1_out, xnor_1_out, xor_1_out;

  not not_1 (not_1_out, entrada);
  not not_2 (not_2_out, chave0);
  buf or_1 (or_1_out, entrada);  // OR_Gate
  not _1 (_1_out, entrada);  // NOR_Gate
  buf _1_2 (_1_2_out, entrada);  // AND_Gate
  not nand_1 (nand_1_out, entrada);  // NAND_Gate
  buf xor_1 (xor_1_out, entrada);  // XOR_Gate
  not xnor_1 (xnor_1_out, entrada);  // XNOR_Gate
  not not_3 (not_3_out, chave1);
  not not_4 (not_4_out, chave2);
  and _2 (_2_out, not_1_out, chave0, chave1, chave2);
  and _3 (_3_out, or_1_out, chave0, chave1, not_4_out);
  and _4 (_4_out, _1_out, not_3_out, not_4_out, chave0);
  and _5 (_5_out, _1_2_out, chave2, chave1, not_2_out);
  and _6 (_6_out, nand_1_out, not_4_out, chave1, not_2_out);
  and _7 (_7_out, xor_1_out, not_3_out, not_2_out, chave2);
  and _8 (_8_out, xnor_1_out, not_2_out, not_3_out, not_4_out);
  or _2_2 (saida, _2_out, _3_out, _4_out, _5_out, _6_out, _7_out, _8_out);

  // Notes on the sheet:
  //   ED 03 
  //   Matricula 449517
  //   Exemplo 0035 - Ana Carolina Conceição de Jesus
  //   chaves 0 1 2
  //   000 - XNOR
  //   001 -  XOR
  //   010 - NAND
  //   011 - AND
  //   100 - NOR
  //   110 -  OR
  //   111 - NOT
  //   Operações
  //   101 - NÃO FAZ NENHUMA OPERAÇÃO
endmodule
