// Logisim project circuito Exemplo0036.circ as structural Verilog: 2 circuits, main circuit main
module main (
  input  a,
  input  b,
  output out_3
);

  wire and_1_out, and_2_out, not_1_out, not_2_out;

  not not_1 (not_1_out, a);
  and and_1 (and_1_out, not_1_out, b);
  and and_2 (and_2_out, a, not_2_out);
  not not_2 (not_2_out, b);
  or or_1 (out_3, and_1_out, and_2_out);

  // Notes on the sheet:
  //   Exercício Extra - ED03 - Exercicio 06
  //   Ana Carolina Conceição de Jesus
  //   Matricula 449517
  //   Comparador pra 2 bits
  //   0 - bists iguais
  //   1 - bits diferentes
endmodule

module \comparador_versão_2  (
  input  a,
  input  b,
  output out_3
);

  xor xor_1 (out_3, a, b);

  // Notes on the sheet:
  //   Exercício Extra - ED03 - Exercicio 06
  //   Ana Carolina Conceição de Jesus
  //   Matricula 449517
  //   versão 2
  //   Comparador pra 2 bits
  //   0 - bists iguais
  //   1 - bits diferentes
endmodule
