// Logisim project circuito Exemplo0037.circ as structural Verilog: 1 circuit, main circuit main
module main (
  input  a,
  input  b,
  output s0,
  output s1,
  output s2
);

  wire not_1_out, not_2_out;

  xnor xnor_1 (s0, a, b);
  not not_1 (not_1_out, b);
  and and_1 (s1, not_1_out, a);
  not not_2 (not_2_out, a);
  and and_2 (s2, not_2_out, b);

  // Notes on the sheet:
  //   Exercício Extra Exemplo0037 - Ana Carolina Conceição de Jesus
  //   a = b , saida em s0
  //   a > b , saida em s1
  //   a < b saida em s2
  //   Matricula 449517
endmodule
