// Logisim project Exercicio02.circ as structural Verilog: 2 circuits, main circuit main
module main (
  input  A,
  input  B,
  input  chave,
  output C
);

  wire AND1_out, OR1_out;

  or OR1 (OR1_out, A, B);
  and AND1 (AND1_out, A, B);
  Multiplexador _0 (.A(OR1_out), .B(AND1_out), .saida(C), .chave(chave));
endmodule

module Multiplexador (
  input  A,
  input  B,
  input  chave,
  output saida
);

  wire AND1_out, AND2_out;

  and AND1 (AND1_out, A, ~chave);  // AND_Gate
  and AND2 (AND2_out, B, chave);
  or OR1 (saida, AND1_out, AND2_out);
endmodule
