// Logisim project Exercicio03.circ as structural Verilog: 2 circuits, main circuit main
module main (
  input  in_1,
  input  A,
  input  B,
  output out_4,
  output out_5
);

  wire and_1_out, not_1_out, not_2_out, or_1_out;

  or or_1 (or_1_out, A, B);
  and and_1 (and_1_out, A, B);
  not not_1 (not_1_out, or_1_out);
  not not_2 (not_2_out, and_1_out);
  Multiplexador multiplexador_1 (.A(or_1_out), .B(not_1_out), .saida(out_4), .chave(in_1));
  Multiplexador multiplexador_2 (.A(and_1_out), .B(not_2_out), .saida(out_5), .chave(in_1));
endmodule

module Multiplexador (
  input  A,
  input  B,
  input  chave,
  output saida
);

  wire AND1_out, AND2_out;

  and AND1 (AND1_out, A, ~chave);  // AND_Gate
  and AND2 (AND2_out, B, chave);
  or OR1 (saida, AND1_out, AND2_out);
endmodule
