// Logisim project Exercicio04.circ as structural Verilog: 2 circuits, main circuit main
module main (
  input  B,
  input  A,
  input  [1:0] chave,
  output out_4
);

  wire multiplexador_1_out_4, multiplexador_2_out_4, nor_1_out, or_1_out, xnor_1_out, xor_1_out;

  or or_1 (or_1_out, B, A);
  nor nor_1 (nor_1_out, B, A);
  xor xor_1 (xor_1_out, B, A);
  xnor xnor_1 (xnor_1_out, B, A);
  multiplexador multiplexador_1 (.in_1(or_1_out), .in_2(nor_1_out), .out_4(multiplexador_1_out_4), .in_3(chave[0]));
  multiplexador multiplexador_2 (.in_1(xor_1_out), .in_2(xnor_1_out), .out_4(multiplexador_2_out_4), .in_3(chave[0]));
  multiplexador multiplexador_3 (
    .in_1(multiplexador_1_out_4), .in_2(multiplexador_2_out_4), .out_4(out_4), .in_3(chave[1]));
endmodule

module multiplexador (
  input  in_1,
  input  in_2,
  input  in_3,
  output out_4
);

  wire and_1_out, and_2_out;

  and and_1 (and_1_out, in_1, ~in_3);  // AND_Gate
  and and_2 (and_2_out, in_2, in_3);
  or or_1 (out_4, and_1_out, and_2_out);
endmodule
