// Logisim project Exercicio05.circ as structural Verilog: 2 circuits, main circuit main
module main (
  input  [2:0] in_1,
  input  A,
  input  B,
  output C
);

  wire AND1_out, multiplexador_1_saida, multiplexador_2_saida, multiplexador_3_saida, multiplexador_4_saida,
       multiplexador_5_saida, multiplexador_6_saida, NAND1_out, NOR1_out, NOT_A_out, NOTB_out, OR1_out,
       XNOR1_out, XOR1_out;

  or OR1 (OR1_out, A, B);
  and AND1 (AND1_out, A, B);
  nor NOR1 (NOR1_out, A, B);
  nand NAND1 (NAND1_out, A, B);
  xnor XNOR1 (XNOR1_out, A, B);
  xor XOR1 (XOR1_out, A, B);
  not NOT_A (NOT_A_out, A);
  not NOTB (NOTB_out, B);
  Multiplexador multiplexador_1 (.A(OR1_out), .B(AND1_out), .saida(multiplexador_1_saida), .chave(in_1[0]));
  Multiplexador multiplexador_2 (.A(NOR1_out), .B(NAND1_out), .saida(multiplexador_2_saida), .chave(in_1[0]));
  Multiplexador multiplexador_3 (.A(XNOR1_out), .B(XOR1_out), .saida(multiplexador_3_saida), .chave(in_1[0]));
  Multiplexador multiplexador_4 (.A(NOT_A_out), .B(NOTB_out), .saida(multiplexador_4_saida), .chave(in_1[0]));
  Multiplexador multiplexador_5 (
    .A(multiplexador_1_saida), .B(multiplexador_2_saida), .saida(multiplexador_5_saida), .chave(in_1[1]));
  Multiplexador multiplexador_6 (
    .A(multiplexador_3_saida), .B(multiplexador_4_saida), .saida(multiplexador_6_saida), .chave(in_1[1]));
  Multiplexador multiplexador_7 (.A(multiplexador_5_saida), .B(multiplexador_6_saida), .saida(C), .chave(in_1[2]));

  // Notes on the sheet:
  //   000
  //   001
  //   010
  //   011
  //   100
  //   101
  //   110
  //   111
endmodule

module Multiplexador (
  input  A,
  input  B,
  input  chave,
  output saida
);

  wire AND1_out, AND2_out;

  and AND1 (AND1_out, A, ~chave);  // AND_Gate
  and AND2 (AND2_out, B, chave);
  or OR1 (saida, AND1_out, AND2_out);
endmodule
