// Logisim project Exercicio06.circ as structural Verilog: 2 circuits, main circuit main
module main (
  input  in_1,
  input  in_2,
  input  [1:0] in_3,
  input  [1:0] in_4,
  input  [2:0] in_5,
  input  [3:0] A,
  input  [3:0] B,
  output out_8,
  output [3:0] C
);

  wire multiplexador_1_saida, multiplexador_2_saida, multiplexador_3_saida, multiplexador_4_saida,
       multiplexador_5_saida, multiplexador_6_saida, multiplexador_7_saida, multiplexador_8_saida,
       multiplexador_9_saida, multiplexador_10_saida, multiplexador_11_saida, multiplexador_12_saida,
       multiplexador_13_saida, multiplexador_14_saida, multiplexador_15_saida, multiplexador_16_saida,
       multiplexador_17_saida, multiplexador_18_saida, multiplexador_19_saida, multiplexador_20_saida,
       multiplexador_21_saida, multiplexador_22_saida, multiplexador_23_saida, multiplexador_24_saida,
       multiplexador_25_saida, multiplexador_26_saida, multiplexador_27_saida, not_1_out, not_2_out,
       or_1_out, or_2_out, XNOR1_out, XNOR2_out;
  wire [3:0] AND1_2_out, NAND1_out, NOR1_out, NOT_A_out, NOTB_out, OR1_out, XNOR1_2_out, XOR1_out;

  xnor XNOR1 (XNOR1_out, in_3[0], in_4[0]);
  xnor XNOR2 (XNOR2_out, in_3[1], in_4[1]);
  not not_1 (not_1_out, XNOR1_out);
  not not_2 (not_2_out, XNOR2_out);
  Multiplexador multiplexador_1 (.A(XNOR1_out), .B(not_1_out), .saida(multiplexador_1_saida), .chave(in_1));
  Multiplexador multiplexador_2 (.A(XNOR2_out), .B(not_2_out), .saida(multiplexador_2_saida), .chave(in_1));
  Multiplexador multiplexador_3 (
    .A(multiplexador_1_saida), .B(multiplexador_2_saida), .saida(multiplexador_3_saida), .chave(in_2));
  or or_1 (or_1_out, multiplexador_3_saida, in_1);
  or or_2 (or_2_out, multiplexador_3_saida, in_1);
  and AND1 (out_8, or_1_out, or_2_out);
  assign OR1_out = A | B;  // OR_Gate OR1, 4 bits wide
  assign AND1_2_out = A & B;  // AND_Gate AND1_2, 4 bits wide
  assign NOR1_out = ~(A | B);  // NOR_Gate NOR1, 4 bits wide
  assign NAND1_out = ~(A & B);  // NAND_Gate NAND1, 4 bits wide
  assign XNOR1_2_out = ~(A ^ B);  // XNOR_Gate XNOR1_2, 4 bits wide
  assign XOR1_out = A ^ B;  // XOR_Gate XOR1, 4 bits wide
  assign NOT_A_out = ~A;  // NOT_Gate NOT_A, 4 bits wide
  assign NOTB_out = ~B;  // NOT_Gate NOTB, 4 bits wide
  Multiplexador multiplexador_4 (.A(OR1_out[0]), .B(AND1_2_out[0]), .saida(multiplexador_4_saida), .chave(in_5[0]));
  Multiplexador multiplexador_5 (.A(OR1_out[1]), .B(AND1_2_out[1]), .saida(multiplexador_5_saida), .chave(in_5[0]));
  Multiplexador multiplexador_6 (.A(OR1_out[2]), .B(AND1_2_out[2]), .saida(multiplexador_6_saida), .chave(in_5[0]));
  Multiplexador multiplexador_7 (.A(OR1_out[3]), .B(AND1_2_out[3]), .saida(multiplexador_7_saida), .chave(in_5[0]));
  Multiplexador multiplexador_8 (.A(NOR1_out[0]), .B(NAND1_out[0]), .saida(multiplexador_8_saida), .chave(in_5[0]));
  Multiplexador multiplexador_9 (.A(NOR1_out[1]), .B(NAND1_out[1]), .saida(multiplexador_9_saida), .chave(in_5[0]));
  Multiplexador multiplexador_10 (.A(NOR1_out[2]), .B(NAND1_out[2]), .saida(multiplexador_10_saida), .chave(in_5[0]));
  Multiplexador multiplexador_11 (.A(NOR1_out[3]), .B(NAND1_out[3]), .saida(multiplexador_11_saida), .chave(in_5[0]));
  Multiplexador multiplexador_12 (.A(XNOR1_2_out[0]), .B(XOR1_out[0]), .saida(multiplexador_12_saida), .chave(in_5[0]));
  Multiplexador multiplexador_13 (.A(XNOR1_2_out[1]), .B(XOR1_out[1]), .saida(multiplexador_13_saida), .chave(in_5[0]));
  Multiplexador multiplexador_14 (.A(XNOR1_2_out[2]), .B(XOR1_out[2]), .saida(multiplexador_14_saida), .chave(in_5[0]));
  Multiplexador multiplexador_15 (.A(XNOR1_2_out[3]), .B(XOR1_out[3]), .saida(multiplexador_15_saida), .chave(in_5[0]));
  Multiplexador multiplexador_16 (.A(NOT_A_out[0]), .B(NOTB_out[0]), .saida(multiplexador_16_saida), .chave(in_5[0]));
  Multiplexador multiplexador_17 (.A(NOT_A_out[1]), .B(NOTB_out[1]), .saida(multiplexador_17_saida), .chave(in_5[0]));
  Multiplexador multiplexador_18 (.A(NOT_A_out[2]), .B(NOTB_out[2]), .saida(multiplexador_18_saida), .chave(in_5[0]));
  Multiplexador multiplexador_19 (.A(NOT_A_out[3]), .B(NOTB_out[3]), .saida(multiplexador_19_saida), .chave(in_5[0]));
  Multiplexador multiplexador_20 (
    .A(multiplexador_4_saida), .B(multiplexador_8_saida), .saida(multiplexador_20_saida), .chave(in_5[1]));
  Multiplexador multiplexador_21 (
    .A(multiplexador_5_saida), .B(multiplexador_9_saida), .saida(multiplexador_21_saida), .chave(in_5[1]));
  Multiplexador multiplexador_22 (
    .A(multiplexador_6_saida), .B(multiplexador_10_saida), .saida(multiplexador_22_saida), .chave(in_5[1]));
  Multiplexador multiplexador_23 (
    .A(multiplexador_7_saida), .B(multiplexador_11_saida), .saida(multiplexador_23_saida), .chave(in_5[1]));
  Multiplexador multiplexador_24 (
    .A(multiplexador_12_saida), .B(multiplexador_16_saida), .saida(multiplexador_24_saida), .chave(in_5[1]));
  Multiplexador multiplexador_25 (
    .A(multiplexador_13_saida), .B(multiplexador_17_saida), .saida(multiplexador_25_saida), .chave(in_5[1]));
  Multiplexador multiplexador_26 (
    .A(multiplexador_14_saida), .B(multiplexador_18_saida), .saida(multiplexador_26_saida), .chave(in_5[1]));
  Multiplexador multiplexador_27 (
    .A(multiplexador_15_saida), .B(multiplexador_19_saida), .saida(multiplexador_27_saida), .chave(in_5[1]));
  Multiplexador multiplexador_28 (
    .A(multiplexador_20_saida), .B(multiplexador_24_saida), .saida(C[0]), .chave(in_5[2]));
  Multiplexador multiplexador_29 (
    .A(multiplexador_21_saida), .B(multiplexador_25_saida), .saida(C[1]), .chave(in_5[2]));
  Multiplexador multiplexador_30 (
    .A(multiplexador_22_saida), .B(multiplexador_26_saida), .saida(C[2]), .chave(in_5[2]));
  Multiplexador multiplexador_31 (
    .A(multiplexador_23_saida), .B(multiplexador_27_saida), .saida(C[3]), .chave(in_5[2]));

  // Notes on the sheet:
  //   110
  //   111
  //   000
  //   001
  //   010
  //   011
  //   100
  //   101
endmodule

module Multiplexador (
  input  A,
  input  B,
  input  chave,
  output saida
);

  wire AND1_out, AND2_out;

  and AND1 (AND1_out, A, ~chave);  // AND_Gate
  and AND2 (AND2_out, B, chave);
  or OR1 (saida, AND1_out, AND2_out);
endmodule
