// Logisim project Exercicio06edit.circ as structural Verilog: 2 circuits, main circuit main
module main (
  input  [1:0] in_1,
  input  [1:0] in_2,
  output out_3
);

  wire xnor_1_out, xnor_2_out;

  xnor xnor_1 (xnor_1_out, in_1[0], in_2[0]);
  xnor xnor_2 (xnor_2_out, in_1[1], in_2[1]);
  nand nand_1 (out_3, xnor_1_out, xnor_2_out);
endmodule

module Multiplexador (
  input  A,
  input  B,
  input  chave,
  output saida
);

  wire AND1_out, AND2_out;

  and AND1 (AND1_out, A, ~chave);  // AND_Gate
  and AND2 (AND2_out, B, chave);
  or OR1 (saida, AND1_out, AND2_out);
endmodule
