// Logisim project TEMP.circ as structural Verilog: 2 circuits, main circuit main
module main (
  input  [3:0] A,
  input  [3:0] B,
  input  [1:0] in_3,
  output [3:0] C
);

  wire multiplexador_1_saida, multiplexador_2_saida, multiplexador_3_saida, multiplexador_4_saida,
       multiplexador_5_saida, multiplexador_6_saida, multiplexador_7_saida, multiplexador_8_saida;
  wire [3:0] AND1_out, NAND1_out, NOR1_out, OR1_out;

  assign OR1_out = A | B;  // OR_Gate OR1, 4 bits wide
  assign AND1_out = A & B;  // AND_Gate AND1, 4 bits wide
  assign NOR1_out = ~(A | B);  // NOR_Gate NOR1, 4 bits wide
  assign NAND1_out = ~(A & B);  // NAND_Gate NAND1, 4 bits wide
  Multiplexador multiplexador_1 (.A(OR1_out[0]), .B(AND1_out[0]), .saida(multiplexador_1_saida), .chave(in_3[1]));
  Multiplexador multiplexador_2 (.A(OR1_out[1]), .B(AND1_out[1]), .saida(multiplexador_2_saida), .chave(in_3[1]));
  Multiplexador multiplexador_3 (.A(OR1_out[2]), .B(AND1_out[2]), .saida(multiplexador_3_saida), .chave(in_3[1]));
  Multiplexador multiplexador_4 (.A(OR1_out[3]), .B(AND1_out[3]), .saida(multiplexador_4_saida), .chave(in_3[1]));
  Multiplexador multiplexador_5 (.A(NOR1_out[0]), .B(NAND1_out[0]), .saida(multiplexador_5_saida), .chave(in_3[1]));
  Multiplexador multiplexador_6 (.A(NOR1_out[1]), .B(NAND1_out[1]), .saida(multiplexador_6_saida), .chave(in_3[1]));
  Multiplexador multiplexador_7 (.A(NOR1_out[2]), .B(NAND1_out[2]), .saida(multiplexador_7_saida), .chave(in_3[1]));
  Multiplexador multiplexador_8 (.A(NOR1_out[3]), .B(NAND1_out[3]), .saida(multiplexador_8_saida), .chave(in_3[1]));
  Multiplexador multiplexador_9 (.A(multiplexador_1_saida), .B(multiplexador_5_saida), .saida(C[0]), .chave(in_3[0]));
  Multiplexador multiplexador_10 (.A(multiplexador_2_saida), .B(multiplexador_6_saida), .saida(C[1]), .chave(in_3[0]));
  Multiplexador multiplexador_11 (.A(multiplexador_3_saida), .B(multiplexador_7_saida), .saida(C[2]), .chave(in_3[0]));
  Multiplexador multiplexador_12 (.A(multiplexador_4_saida), .B(multiplexador_8_saida), .saida(C[3]), .chave(in_3[0]));
endmodule

module Multiplexador (
  input  A,
  input  B,
  input  chave,
  output saida
);

  wire AND1_out, AND2_out;

  and AND1 (AND1_out, A, ~chave);  // AND_Gate
  and AND2 (AND2_out, B, chave);
  or OR1 (saida, AND1_out, AND2_out);
endmodule
