// Logisim project TEMP2.circ as structural Verilog: 2 circuits, main circuit main
module main (
  input  [2:0] in_1,
  input  [3:0] A,
  input  [3:0] B,
  output [3:0] C
);

  wire multiplexador_1_saida, multiplexador_2_saida, multiplexador_3_saida, multiplexador_4_saida,
       multiplexador_5_saida, multiplexador_6_saida, multiplexador_7_saida, multiplexador_8_saida,
       multiplexador_9_saida, multiplexador_10_saida, multiplexador_11_saida, multiplexador_12_saida,
       multiplexador_13_saida, multiplexador_14_saida, multiplexador_15_saida, multiplexador_16_saida,
       multiplexador_17_saida, multiplexador_18_saida, multiplexador_19_saida, multiplexador_20_saida,
       multiplexador_21_saida, multiplexador_22_saida, multiplexador_23_saida, multiplexador_24_saida;
  wire [3:0] AND1_out, NAND1_out, NOR1_out, NOT_A_out, NOTB_out, OR1_out, XNOR1_out, XOR1_out;

  assign OR1_out = A | B;  // OR_Gate OR1, 4 bits wide
  assign AND1_out = A & B;  // AND_Gate AND1, 4 bits wide
  assign NOR1_out = ~(A | B);  // NOR_Gate NOR1, 4 bits wide
  assign NAND1_out = ~(A & B);  // NAND_Gate NAND1, 4 bits wide
  assign XNOR1_out = ~(A ^ B);  // XNOR_Gate XNOR1, 4 bits wide
  assign XOR1_out = A ^ B;  // XOR_Gate XOR1, 4 bits wide
  assign NOT_A_out = ~A;  // NOT_Gate NOT_A, 4 bits wide
  assign NOTB_out = ~B;  // NOT_Gate NOTB, 4 bits wide
  Multiplexador multiplexador_1 (.A(OR1_out[0]), .B(AND1_out[0]), .saida(multiplexador_1_saida), .chave(in_1[0]));
  Multiplexador multiplexador_2 (.A(OR1_out[1]), .B(AND1_out[1]), .saida(multiplexador_2_saida), .chave(in_1[0]));
  Multiplexador multiplexador_3 (.A(OR1_out[2]), .B(AND1_out[2]), .saida(multiplexador_3_saida), .chave(in_1[0]));
  Multiplexador multiplexador_4 (.A(OR1_out[3]), .B(AND1_out[3]), .saida(multiplexador_4_saida), .chave(in_1[0]));
  Multiplexador multiplexador_5 (.A(NOR1_out[0]), .B(NAND1_out[0]), .saida(multiplexador_5_saida), .chave(in_1[0]));
  Multiplexador multiplexador_6 (.A(NOR1_out[1]), .B(NAND1_out[1]), .saida(multiplexador_6_saida), .chave(in_1[0]));
  Multiplexador multiplexador_7 (.A(NOR1_out[2]), .B(NAND1_out[2]), .saida(multiplexador_7_saida), .chave(in_1[0]));
  Multiplexador multiplexador_8 (.A(NOR1_out[3]), .B(NAND1_out[3]), .saida(multiplexador_8_saida), .chave(in_1[0]));
  Multiplexador multiplexador_9 (.A(XNOR1_out[0]), .B(XOR1_out[0]), .saida(multiplexador_9_saida), .chave(in_1[0]));
  Multiplexador multiplexador_10 (.A(XNOR1_out[1]), .B(XOR1_out[1]), .saida(multiplexador_10_saida), .chave(in_1[0]));
  Multiplexador multiplexador_11 (.A(XNOR1_out[2]), .B(XOR1_out[2]), .saida(multiplexador_11_saida), .chave(in_1[0]));
  Multiplexador multiplexador_12 (.A(XNOR1_out[3]), .B(XOR1_out[3]), .saida(multiplexador_12_saida), .chave(in_1[0]));
  Multiplexador multiplexador_13 (.A(NOT_A_out[0]), .B(NOTB_out[0]), .saida(multiplexador_13_saida), .chave(in_1[0]));
  Multiplexador multiplexador_14 (.A(NOT_A_out[1]), .B(NOTB_out[1]), .saida(multiplexador_14_saida), .chave(in_1[0]));
  Multiplexador multiplexador_15 (.A(NOT_A_out[2]), .B(NOTB_out[2]), .saida(multiplexador_15_saida), .chave(in_1[0]));
  Multiplexador multiplexador_16 (.A(NOT_A_out[3]), .B(NOTB_out[3]), .saida(multiplexador_16_saida), .chave(in_1[0]));
  Multiplexador multiplexador_17 (
    .A(multiplexador_1_saida), .B(multiplexador_5_saida), .saida(multiplexador_17_saida), .chave(in_1[1]));
  Multiplexador multiplexador_18 (
    .A(multiplexador_2_saida), .B(multiplexador_6_saida), .saida(multiplexador_18_saida), .chave(in_1[1]));
  Multiplexador multiplexador_19 (
    .A(multiplexador_3_saida), .B(multiplexador_7_saida), .saida(multiplexador_19_saida), .chave(in_1[1]));
  Multiplexador multiplexador_20 (
    .A(multiplexador_4_saida), .B(multiplexador_8_saida), .saida(multiplexador_20_saida), .chave(in_1[1]));
  Multiplexador multiplexador_21 (
    .A(multiplexador_9_saida), .B(multiplexador_13_saida), .saida(multiplexador_21_saida), .chave(in_1[1]));
  Multiplexador multiplexador_22 (
    .A(multiplexador_10_saida), .B(multiplexador_14_saida), .saida(multiplexador_22_saida), .chave(in_1[1]));
  Multiplexador multiplexador_23 (
    .A(multiplexador_11_saida), .B(multiplexador_15_saida), .saida(multiplexador_23_saida), .chave(in_1[1]));
  Multiplexador multiplexador_24 (
    .A(multiplexador_12_saida), .B(multiplexador_16_saida), .saida(multiplexador_24_saida), .chave(in_1[1]));
  Multiplexador multiplexador_25 (
    .A(multiplexador_17_saida), .B(multiplexador_21_saida), .saida(C[0]), .chave(in_1[2]));
  Multiplexador multiplexador_26 (
    .A(multiplexador_18_saida), .B(multiplexador_22_saida), .saida(C[1]), .chave(in_1[2]));
  Multiplexador multiplexador_27 (
    .A(multiplexador_19_saida), .B(multiplexador_23_saida), .saida(C[2]), .chave(in_1[2]));
  Multiplexador multiplexador_28 (
    .A(multiplexador_20_saida), .B(multiplexador_24_saida), .saida(C[3]), .chave(in_1[2]));

  // Notes on the sheet:
  //   000
  //   001
  //   010
  //   011
  //   100
  //   101
  //   110
  //   111
endmodule

module Multiplexador (
  input  A,
  input  B,
  input  chave,
  output saida
);

  wire AND1_out, AND2_out;

  and AND1 (AND1_out, A, ~chave);  // AND_Gate
  and AND2 (AND2_out, B, chave);
  or OR1 (saida, AND1_out, AND2_out);
endmodule
