// Logisim project exemplo0032.circ as structural Verilog: 1 circuit, main circuit main
module main (
  input  a,
  input  b,
  input  in_3,
  output s
);

  wire AND_2_out, AND_3_out, AND_out, not_1_out, OR_out;

  and AND (AND_out, a, b);
  or OR (OR_out, a, b);
  not not_1 (not_1_out, in_3);
  and AND_2 (AND_2_out, AND_out, in_3);
  and AND_3 (AND_3_out, OR_out, not_1_out);
  or OR_2 (s, AND_2_out, AND_3_out);

  // Notes on the sheet:
  //   temp1
  //   temp2
  //   temp3
  //   temp4
endmodule
