// Logisim project exemplo0033.circ as structural Verilog: 1 circuit, main circuit main
module main (
  input  a,
  input  b,
  input  in_3,
  output out_4,
  output s
);

  wire AND_2_out, AND_3_out, AND_4_out, AND_5_out, AND_out, NAND_out, NOR_out, not_1_out, OR_out;

  nand NAND (NAND_out, a, b);
  nor NOR (NOR_out, a, b);
  and AND (AND_out, a, b);
  or OR (OR_out, a, b);
  not not_1 (not_1_out, in_3);
  and AND_2 (AND_2_out, NAND_out, in_3);
  and AND_3 (AND_3_out, AND_out, not_1_out);
  and AND_4 (AND_4_out, NOR_out, in_3);
  and AND_5 (AND_5_out, OR_out, not_1_out);
  or OR_2 (out_4, AND_2_out, AND_3_out);
  or OR_3 (s, AND_4_out, AND_5_out);
endmodule
