// Logisim project exemplo0034.circ as structural Verilog: 1 circuit, main circuit main
module main (
  input  a,
  input  b,
  input  in_3,
  input  in_4,
  output s
);

  wire AND_2_out, AND_3_out, AND_4_out, AND_5_out, AND_6_out, AND_out, NOR_out, not_1_out, not_2_out,
       OR_2_out, OR_3_out, OR_out, XNOR_out, XOR_out;

  xnor XNOR (XNOR_out, b, a);
  xor XOR (XOR_out, a, b);
  nor NOR (NOR_out, a, b);
  or OR (OR_out, a, b);
  not not_1 (not_1_out, in_3);
  and AND (AND_out, XNOR_out, in_3);
  and AND_2 (AND_2_out, XOR_out, in_3);
  and AND_3 (AND_3_out, NOR_out, not_1_out);
  and AND_4 (AND_4_out, OR_out, not_1_out);
  or OR_2 (OR_2_out, AND_out, AND_3_out);
  or OR_3 (OR_3_out, AND_2_out, AND_4_out);
  not not_2 (not_2_out, in_4);
  and AND_5 (AND_5_out, OR_2_out, in_4);
  and AND_6 (AND_6_out, OR_3_out, not_2_out);
  or OR_4 (s, AND_5_out, AND_6_out);
endmodule
