// Logisim project Exemplo0031.circ as structural Verilog: 1 circuit, main circuit main
module main (
  input  [3:0] A,
  input  [3:0] B,
  output [3:0] S1,
  output [3:0] S2
);

  assign S1 = A & A & B;  // AND_Gate AND, 4 bits wide
  assign S2 = A | B;  // OR_Gate OR, 4 bits wide
endmodule
