// Logisim project Exemplo0033.circ as structural Verilog: 1 circuit, main circuit main
module main (
  input  a,
  input  b,
  input  CHAVE,
  output s2,
  output s1
);

  wire AND_2_out, AND_3_out, AND_4_out, AND_5_out, AND_out, NAND_out, NOR_out, not_1_out, OR_out;

  nor NOR (NOR_out, a, b);
  nand NAND (NAND_out, b, a);
  and AND (AND_out, a, b);
  or OR (OR_out, a, b);
  not not_1 (not_1_out, CHAVE);
  and AND_2 (AND_2_out, NOR_out, CHAVE);
  and AND_3 (AND_3_out, NAND_out, CHAVE);
  and AND_4 (AND_4_out, AND_out, not_1_out);
  and AND_5 (AND_5_out, OR_out, not_1_out);
  or OR_2 (s1, AND_3_out, AND_5_out);
  or OR_3 (s2, AND_2_out, AND_4_out);

  // Notes on the sheet:
  //   temp6
  //   temp5
  //   temp1
  //   temp2
  //   NOT
  //   temp8
  //   temp7
  //   temp3
  //   temp4
endmodule
