// Logisim project Exemplo0035.circ as structural Verilog: 1 circuit, main circuit main
module main (
  input  a,
  input  b,
  input  CHAVE1,
  input  CHAVE2,
  input  CHAVE3,
  output s
);

  wire AND_2_out, AND_3_out, AND_4_out, AND_5_out, AND_6_out, AND_7_out, AND_8_out, AND_9_out, AND_10_out,
       AND_11_out, AND_12_out, AND_13_out, AND_out, NAND_out, NOR_out, not_1_out, not_2_out, not_3_out,
       not_4_out, OR_2_out, OR_3_out, OR_4_out, OR_5_out, OR_6_out, OR_out, XNOR_out, XOR_out;

  or OR (OR_out, b, a);
  nor NOR (NOR_out, b, a);
  and AND (AND_out, b, a);
  nand NAND (NAND_out, b, a);
  not not_1 (not_1_out, a);
  xor XOR (XOR_out, b, a);
  xnor XNOR (XNOR_out, b, a);
  not not_2 (not_2_out, CHAVE1);
  and AND_2 (AND_2_out, CHAVE1, OR_out);
  and AND_3 (AND_3_out, not_2_out, NOR_out);
  and AND_4 (AND_4_out, CHAVE1, AND_out);
  and AND_5 (AND_5_out, not_2_out, NAND_out);
  and AND_6 (AND_6_out, XOR_out, CHAVE1);
  and AND_7 (AND_7_out, XNOR_out, not_2_out);
  or OR_2 (OR_2_out, AND_2_out, AND_3_out);
  or OR_3 (OR_3_out, AND_4_out, AND_5_out);
  or OR_4 (OR_4_out, AND_6_out, AND_7_out);
  not not_3 (not_3_out, CHAVE2);
  and AND_8 (AND_8_out, CHAVE2, OR_2_out);
  and AND_9 (AND_9_out, not_3_out, OR_3_out);
  and AND_10 (AND_10_out, not_1_out, CHAVE2);
  and AND_11 (AND_11_out, not_3_out, OR_4_out);
  or OR_5 (OR_5_out, AND_8_out, AND_9_out);
  or OR_6 (OR_6_out, AND_10_out, AND_11_out);
  and AND_12 (AND_12_out, OR_5_out, CHAVE3);
  and AND_13 (AND_13_out, not_4_out, OR_6_out);
  not not_4 (not_4_out, CHAVE3);
  or OR_7 (s, AND_12_out, AND_13_out);

  // Notes on the sheet:
  //   temp1
  //   temp2
  //   temp3
  //   temp4
  //   temp5
  //   temp6
  //   temp7
  //   temp8
  //   temp9
  //   temp10
  //   temp11
  //   temp12
  //   NOT
  //   temp13
  //   temp14
  //   temp15
  //   temp16
  //   temp17
  //   temp18
  //   temp19
  //   temp20
  //   temp21
  //   temp22
  //   temp23
endmodule
