// Logisim project Logisin 03.circ as structural Verilog
module Multiplexador (
  input  A,
  input  B,
  input  Chave,
  output S
);

  wire and_1_out, and_2_out, not_1_out;

  not not_1 (not_1_out, Chave);
  and and_1 (and_1_out, A, not_1_out);
  and and_2 (and_2_out, B, Chave);
  or or_1 (S, and_1_out, and_2_out);
endmodule

module Exemplo_31 (
  input  [3:0] in_1,
  input  [3:0] in_2,
  output [3:0] out_3,
  output [3:0] out_4
);

  assign out_3 = in_1 & in_2;  // AND_Gate and_1, 4 bits wide
  assign out_4 = in_1 | in_2;  // OR_Gate or_1, 4 bits wide
endmodule

module Exemplo_32 (
  input  A,
  input  B,
  input  Chave,
  output S
);

  wire and_1_out, or_1_out;

  and and_1 (and_1_out, A, B);
  or or_1 (or_1_out, A, B);
  Multiplexador multiplexador_1 (.A(and_1_out), .B(or_1_out), .Chave(Chave), .S(S));
endmodule

module Exemplo_33 (
  input  in_1,
  input  in_2,
  input  in_3,
  output out_4,
  output out_5
);

  wire and_1_out, nand_1_out, nor_1_out, or_1_out;

  and and_1 (and_1_out, in_2, in_1);
  nand nand_1 (nand_1_out, in_1, in_2);
  or or_1 (or_1_out, in_2, in_1);
  nor nor_1 (nor_1_out, in_1, in_2);
  Multiplexador multiplexador_1 (.A(and_1_out), .B(nand_1_out), .Chave(in_3), .S(out_4));
  Multiplexador multiplexador_2 (.A(or_1_out), .B(nor_1_out), .Chave(in_3), .S(out_5));
endmodule

module Exemplo_34 (
  input  in_1,
  input  in_2,
  input  [1:0] in_3,
  output out_4
);

  wire multiplexador_1_s, multiplexador_2_s, nor_1_out, or_1_out, xnor_1_out, xor_1_out;

  xnor xnor_1 (xnor_1_out, in_2, in_1);
  nor nor_1 (nor_1_out, in_1, in_2);
  xor xor_1 (xor_1_out, in_2, in_1);
  or or_1 (or_1_out, in_2, in_1);
  Multiplexador multiplexador_1 (.A(xnor_1_out), .B(nor_1_out), .Chave(in_3[0]), .S(multiplexador_1_s));
  Multiplexador multiplexador_2 (.A(xor_1_out), .B(or_1_out), .Chave(in_3[0]), .S(multiplexador_2_s));
  Multiplexador multiplexador_3 (.A(multiplexador_2_s), .B(multiplexador_1_s), .Chave(in_3[1]), .S(out_4));
endmodule

module Exemplo_35 (
  input  in_1,
  input  in_2,
  input  [2:0] in_3,
  output out_4
);

  wire and_1_out, multiplexador_1_s, multiplexador_2_s, multiplexador_3_s, multiplexador_4_s,
       multiplexador_5_s, multiplexador_6_s, nand_1_out, nor_1_out, not_1_out, not_2_out, or_1_out,
       xnor_1_out, xor_1_out;

  or or_1 (or_1_out, in_2, in_1);
  and and_1 (and_1_out, in_2, in_1);
  nor nor_1 (nor_1_out, in_2, in_1);
  nand nand_1 (nand_1_out, in_2, in_1);
  xor xor_1 (xor_1_out, in_2, in_1);
  xnor xnor_1 (xnor_1_out, in_2, in_1);
  not not_1 (not_1_out, in_2);
  not not_2 (not_2_out, in_1);
  Multiplexador multiplexador_1 (.A(or_1_out), .B(and_1_out), .Chave(in_3[2]), .S(multiplexador_1_s));
  Multiplexador multiplexador_2 (.A(nor_1_out), .B(nand_1_out), .Chave(in_3[2]), .S(multiplexador_2_s));
  Multiplexador multiplexador_3 (.A(xor_1_out), .B(xnor_1_out), .Chave(in_3[2]), .S(multiplexador_3_s));
  Multiplexador multiplexador_4 (.A(not_1_out), .B(not_2_out), .Chave(in_3[2]), .S(multiplexador_4_s));
  Multiplexador multiplexador_5 (.A(multiplexador_1_s), .B(multiplexador_2_s), .Chave(in_3[1]), .S(multiplexador_5_s));
  Multiplexador multiplexador_6 (.A(multiplexador_3_s), .B(multiplexador_4_s), .Chave(in_3[1]), .S(multiplexador_6_s));
  Multiplexador multiplexador_7 (.A(multiplexador_5_s), .B(multiplexador_6_s), .Chave(in_3[0]), .S(out_4));
endmodule
