// Logisim project Exercicio01.circ as structural Verilog: 1 circuit, main circuit main
module main (
  input  [3:0] in_1,
  input  [3:0] in_2,
  output [3:0] out_3,
  output [3:0] out_4
);

  assign out_3 = in_2 & in_1;  // AND_Gate and_1, 4 bits wide
  assign out_4 = in_2 | in_1;  // OR_Gate or_1, 4 bits wide

  // Notes on the sheet:
  //   Guilherme Augusto Bueno Borba-451564
endmodule
