// Logisim project Exercicio02.circ as structural Verilog: 2 circuits, main circuit main
module main (
  input  in_1,
  input  in_2,
  input  _1_porta_and,
  output out_4
);

  wire and_1_out, or_1_out;

  and and_1 (and_1_out, in_1, in_2);
  or or_1 (or_1_out, in_2, in_1);
  mux mux_1 (.in_1(and_1_out), .in_2(or_1_out), .in_3(_1_porta_and), .out_4(out_4));

  // Notes on the sheet:
  //   Guilherme Augusto Bueno Borba-451564
  //   0 porta or
endmodule

module mux (
  input  in_1,
  input  in_2,
  input  in_3,
  output out_4
);

  wire and_1_out, and_2_out, not_1_out;

  not not_1 (not_1_out, in_3);
  and and_1 (and_1_out, in_1, not_1_out);
  and and_2 (and_2_out, in_3, in_2);
  or or_1 (out_4, and_1_out, and_2_out);
endmodule
