// Logisim project Exercicio03.circ as structural Verilog: 1 circuit, main circuit main
module main (
  input  a,
  input  b,
  input  c,
  output s1,
  output s2
);

  wire and_1_out, and_2_out, and_3_out, and_4_out, and_5_out, nand_1_out, nor_1_out, not_1_out, or_1_out;

  nor nor_1 (nor_1_out, a, b);
  or or_1 (or_1_out, a, b);
  nand nand_1 (nand_1_out, a, b);
  and and_1 (and_1_out, a, b);
  not not_1 (not_1_out, c);
  and and_2 (and_2_out, nor_1_out, not_1_out);
  and and_3 (and_3_out, or_1_out, c);
  and and_4 (and_4_out, nand_1_out, not_1_out);
  and and_5 (and_5_out, c, and_1_out);
  or or_2 (s1, and_2_out, and_3_out);
  or or_3 (s2, and_4_out, and_5_out);

  // Notes on the sheet:
  //   Guilherme Augusto Bueno Borba-451564
endmodule
