// Logisim project Exercicio04.circ as structural Verilog: 1 circuit, main circuit main
module main (
  input  a,
  input  b,
  input  c1,
  input  c2,
  output out_5,
  output out_6
);

  wire and_1_out, and_2_out, and_3_out, and_4_out, nor_1_out, not_1_out, not_2_out, not_3_out, not_4_out,
       or_1_out, xnor_1_out, xor_1_out;

  xor xor_1 (xor_1_out, b, a);
  xnor xnor_1 (xnor_1_out, b, a);
  or or_1 (or_1_out, b, a);
  nor nor_1 (nor_1_out, b, a);
  and and_1 (and_1_out, xor_1_out, c1, not_1_out);
  not not_1 (not_1_out, c2);
  and and_2 (and_2_out, xnor_1_out, c1, c2);
  not not_2 (not_2_out, c1);
  and and_3 (and_3_out, or_1_out, not_2_out, not_3_out);
  not not_3 (not_3_out, c2);
  and and_4 (and_4_out, nor_1_out, not_4_out, c2);
  not not_4 (not_4_out, c1);
  or or_2 (out_5, and_1_out, and_2_out);
  or or_3 (out_6, and_3_out, and_4_out);

  // Notes on the sheet:
  //   Guilherme Augusto Bueno Borba-451564
endmodule
