// Logisim project Exercicio05.circ as structural Verilog: 1 circuit, main circuit main
module main (
  input  a,
  input  b,
  input  c1,
  input  c2,
  input  c3,
  output out_6,
  output out_7,
  output out_8,
  output out_9
);

  wire and_1_out, and_2_out, and_3_out, and_4_out, and_5_out, and_6_out, and_7_out, and_8_out, and_9_out,
       nand_1_out, nor_1_out, not_1_out, not_2_out, not_3_out, not_4_out, not_5_out, not_6_out, not_7_out,
       not_8_out, not_9_out, not_10_out, not_11_out, not_12_out, not_13_out, not_14_out, or_1_out,
       xnor_1_out, xor_1_out;

  not not_1 (not_1_out, a);
  not not_2 (not_2_out, b);
  or or_1 (or_1_out, a, b);
  and and_1 (and_1_out, a, b);
  xor xor_1 (xor_1_out, a, b);
  nor nor_1 (nor_1_out, a, b);
  nand nand_1 (nand_1_out, a, b);
  xnor xnor_1 (xnor_1_out, a, b);
  not not_3 (not_3_out, c1);
  not not_4 (not_4_out, c2);
  not not_5 (not_5_out, c3);
  not not_6 (not_6_out, c1);
  not not_7 (not_7_out, c2);
  not not_8 (not_8_out, c1);
  not not_9 (not_9_out, c3);
  not not_10 (not_10_out, c1);
  not not_11 (not_11_out, c2);
  not not_12 (not_12_out, c3);
  not not_13 (not_13_out, c2);
  not not_14 (not_14_out, c3);
  and and_2 (and_2_out, not_1_out, not_3_out, not_4_out, not_5_out);
  and and_3 (and_3_out, not_2_out, not_6_out, not_7_out, c3);
  and and_4 (and_4_out, or_1_out, not_8_out, c2, not_9_out);
  and and_5 (and_5_out, nor_1_out, not_10_out, c2, c3);
  and and_6 (and_6_out, and_1_out, c1, not_11_out, not_12_out);
  and and_7 (and_7_out, nand_1_out, c1, not_13_out, c3);
  and and_8 (and_8_out, xor_1_out, c1, c2, not_14_out);
  and and_9 (and_9_out, xnor_1_out, c1, c2, c3);
  or or_2 (out_6, and_2_out, and_3_out);
  or or_3 (out_7, and_4_out, and_5_out);
  or or_4 (out_8, and_6_out, and_7_out);
  or or_5 (out_9, and_8_out, and_9_out);

  // Notes on the sheet:
  //   Guilherme Augusto Bueno Borba 451564
endmodule
