// Logisim project Exemplo0033.circ as structural Verilog: 1 circuit, main circuit main
module main (
  input  in_1,
  input  in_2,
  input  in_3,
  input  in_4,
  input  in_5,
  input  in_6,
  output out_7,
  output out_8,
  output out_9,
  output out_10
);

  wire and_1_out, and_2_out, and_3_out, and_4_out, and_5_out, and_6_out, nand_1_out, nand_2_out, nor_1_out,
       nor_2_out, not_1_out, or_1_out, or_2_out;

  and and_1 (and_1_out, in_2, in_1);
  or or_1 (or_1_out, in_1, in_2);
  nand nand_1 (nand_1_out, in_2, in_1);
  nor nor_1 (nor_1_out, in_2, in_1);
  and and_2 (and_2_out, in_5, in_4);
  or or_2 (or_2_out, in_4, in_5);
  nand nand_2 (nand_2_out, in_5, in_4);
  nor nor_2 (nor_2_out, in_5, in_4);
  not not_1 (not_1_out, in_3);
  and and_3 (and_3_out, and_1_out, in_3);
  and and_4 (and_4_out, or_1_out, in_3);
  and and_5 (and_5_out, nand_1_out, not_1_out);
  and and_6 (and_6_out, nor_1_out, not_1_out);
  Multiplexer #(.enable("false")) multiplexer_1 (.in0(and_2_out), .in1(nand_2_out), .out(out_9), .sel(in_6));
  Multiplexer #(.enable("false")) multiplexer_2 (.in0(or_2_out), .in1(nor_2_out), .out(out_10), .sel(in_6));
  or or_3 (out_7, and_3_out, and_5_out);
  or or_4 (out_8, and_4_out, and_6_out);
endmodule
