// Logisim project Ex03.circ as structural Verilog: 2 circuits, main circuit main
module main (
  input  a,
  input  b,
  input  chave,
  output s0,
  output s1
);

  wire and_1_out, nand_1_out, nor_1_out, or_1_out;

  and and_1 (and_1_out, a, b);
  nand nand_1 (nand_1_out, b, a);
  or or_1 (or_1_out, a, b);
  nor nor_1 (nor_1_out, a, b);
  multiplexador multiplexador_1 (.a(and_1_out), .b(nand_1_out), .chave(chave), .out_4(s0));
  multiplexador multiplexador_2 (.a(or_1_out), .b(nor_1_out), .chave(chave), .out_4(s1));
endmodule

module multiplexador (
  input  a,
  input  b,
  input  chave,
  output out_4
);

  wire and_1_out, and_2_out, not_1_out;

  and and_1 (and_1_out, a, not_1_out);
  not not_1 (not_1_out, chave);
  and and_2 (and_2_out, b, chave);
  or or_1 (out_4, and_1_out, and_2_out);
endmodule
