// Logisim project Ex04.circ as structural Verilog: 2 circuits, main circuit main
module main (
  input  a,
  input  b,
  input  [1:0] chave,
  output s0
);

  wire multiplexador_1_out_4, multiplexador_2_out_4, nor_1_out, or_1_out, xnor_1_out, xor_1_out;

  xor xor_1 (xor_1_out, a, b);
  or or_1 (or_1_out, b, a);
  xnor xnor_1 (xnor_1_out, a, b);
  nor nor_1 (nor_1_out, a, b);
  multiplexador multiplexador_1 (.a(xor_1_out), .b(or_1_out), .chave(chave[0]), .out_4(multiplexador_1_out_4));
  multiplexador multiplexador_2 (.a(xnor_1_out), .b(nor_1_out), .chave(chave[0]), .out_4(multiplexador_2_out_4));
  multiplexador multiplexador_3 (.a(multiplexador_1_out_4), .b(multiplexador_2_out_4), .chave(chave[1]), .out_4(s0));
endmodule

module multiplexador (
  input  a,
  input  b,
  input  chave,
  output out_4
);

  wire and_1_out, and_2_out, not_1_out;

  and and_1 (and_1_out, a, not_1_out);
  not not_1 (not_1_out, chave);
  and and_2 (and_2_out, b, chave);
  or or_1 (out_4, and_1_out, and_2_out);
endmodule
