// Logisim project Ex05.circ as structural Verilog: 2 circuits, main circuit main
module main (
  input  a,
  input  b,
  input  [2:0] chave,
  output s0
);

  wire and_1_out, multiplexador_1_out_4, multiplexador_2_out_4, multiplexador_3_out_4, multiplexador_4_out_4,
       multiplexador_5_out_4, multiplexador_6_out_4, nand_1_out, nor_1_out, not_1_out, not_2_out, or_1_out,
       xnor_1_out, xor_1_out;

  or or_1 (or_1_out, a, b);
  and and_1 (and_1_out, b, a);
  nor nor_1 (nor_1_out, a, b);
  nand nand_1 (nand_1_out, a, b);
  xor xor_1 (xor_1_out, a, a);
  xnor xnor_1 (xnor_1_out, a, a);
  not not_1 (not_1_out, a);
  not not_2 (not_2_out, a);
  multiplexador multiplexador_1 (.a(or_1_out), .b(and_1_out), .chave(chave[0]), .out_4(multiplexador_1_out_4));
  multiplexador multiplexador_2 (.a(nor_1_out), .b(nand_1_out), .chave(chave[0]), .out_4(multiplexador_2_out_4));
  multiplexador multiplexador_3 (.a(xor_1_out), .b(xnor_1_out), .chave(chave[0]), .out_4(multiplexador_3_out_4));
  multiplexador multiplexador_4 (.a(not_1_out), .b(not_2_out), .chave(chave[0]), .out_4(multiplexador_4_out_4));
  multiplexador multiplexador_5 (
    .a(multiplexador_1_out_4), .b(multiplexador_2_out_4), .chave(chave[1]), .out_4(multiplexador_5_out_4));
  multiplexador multiplexador_6 (
    .a(multiplexador_3_out_4), .b(multiplexador_4_out_4), .chave(chave[1]), .out_4(multiplexador_6_out_4));
  multiplexador multiplexador_7 (.a(multiplexador_5_out_4), .b(multiplexador_6_out_4), .chave(chave[2]), .out_4(s0));
endmodule

module multiplexador (
  input  a,
  input  b,
  input  chave,
  output out_4
);

  wire and_1_out, and_2_out, not_1_out;

  and and_1 (and_1_out, a, not_1_out);
  not not_1 (not_1_out, chave);
  and and_2 (and_2_out, b, chave);
  or or_1 (out_4, and_1_out, and_2_out);
endmodule
