// Logisim project exemplo0032.circ as structural Verilog: 1 circuit, main circuit main
module main (
  input  in_1,
  input  in_2,
  input  in_3,
  output out_4
);

  wire and_1_out, and_2_out, and_3_out, not_1_out, or_1_out;

  and and_1 (and_1_out, in_1, in_2);
  or or_1 (or_1_out, in_1, in_2);
  not not_1 (not_1_out, in_3);
  and and_2 (and_2_out, and_1_out, not_1_out);
  and and_3 (and_3_out, or_1_out, or_1_out, in_3);
  or or_2 (out_4, and_2_out, and_2_out, and_3_out, and_3_out);
endmodule
