// Logisim project Exemplo0031.circ as structural Verilog: 1 circuit, main circuit main
module main (
  input  [3:0] in_1,
  input  [3:0] in_2,
  output [3:0] out_3,
  output [3:0] out_4
);

  and and_1 (out_3[0], in_2[0], in_1[0]);
  and and_2 (out_3[1], in_2[1], in_1[1]);
  and and_3 (out_3[2], in_2[2], in_1[2]);
  and and_4 (out_3[3], in_2[3], in_1[3]);
  or or_1 (out_4[0], in_2[0], in_1[0]);
  or or_2 (out_4[1], in_2[1], in_1[1]);
  or or_3 (out_4[2], in_2[2], in_1[2]);
  or or_4 (out_4[3], in_2[3], in_1[3]);
endmodule
