// Logisim project Exemplo0031.circ as structural Verilog: 1 circuit, main circuit main
module main (
  input  [2:0] A,
  input  [2:0] B,
  output [2:0] out_3
);


  assign B = A;
  assign out_3 = A;
endmodule
