// Logisim project Exemplo0032.circ as structural Verilog: 1 circuit, main circuit main
module main (
  input  A,
  input  B,
  input  Chave,
  output S1
);

  wire And1_out, And2_out, And3_out, not_1_out, Or1_out;

  and And1 (And1_out, A, B);
  or Or1 (Or1_out, A, B);
  not not_1 (not_1_out, Chave);
  and And2 (And2_out, And1_out, And1_out, not_1_out);
  and And3 (And3_out, Chave, Or1_out);
  or Or2 (S1, And2_out, And3_out);

  // Notes on the sheet:
  //   temp1
  //   notchave
  //   temp2
  //   tmp3
  //   tmp4
endmodule
