// Logisim project Exemplo0033.circ as structural Verilog: 1 circuit, main circuit main
module main (
  input  B,
  input  A,
  input  Chave,
  output S1
);

  wire And2_out, And3_out, and_1_out, nand_1_out, nor_1_out, not_1_out, or_1_out;

  and and_1 (and_1_out, A, B);
  or or_1 (or_1_out, A, B);
  nand nand_1 (nand_1_out, A, B);
  nor nor_1 (nor_1_out, A, B);
  not not_1 (not_1_out, Chave);
  and And2 (And2_out, and_1_out, and_1_out, or_1_out, not_1_out);
  and And3 (And3_out, Chave, nand_1_out, nor_1_out);
  or Or2 (S1, And2_out, And3_out);

  // Notes on the sheet:
  //   temp1
  //   temp2
  //   tenp3
  //   temp4
  //   notchave
  //   temp6
  //   temp5
  //   temp6
  //   temp7
endmodule
