// Logisim project Exemplo0034.circ as structural Verilog: 1 circuit, main circuit main
module main (
  input  B,
  input  A,
  input  [1:0] Chave,
  output S1
);

  wire AND1_out, AND2_out, AND3_out, AND4_out, NOR1_out, NOT1_out, NOT2_out, NOT3_out, NOt4_out, OR1_out,
       XNOR1_out, XOR1_out;

  or OR1 (OR1_out, A, B);
  nor NOR1 (NOR1_out, A, B);
  xor XOR1 (XOR1_out, A, B);
  xnor XNOR1 (XNOR1_out, A, B);
  not NOT1 (NOT1_out, Chave[1]);
  not NOT2 (NOT2_out, Chave[0]);
  not NOT3 (NOT3_out, Chave[1]);
  not NOt4 (NOt4_out, Chave[0]);
  and AND1 (AND1_out, OR1_out, NOT1_out, NOT2_out);
  and AND2 (AND2_out, NOR1_out, NOT3_out, Chave[0]);
  and AND3 (AND3_out, XOR1_out, Chave[1], NOt4_out);
  and AND4 (AND4_out, XNOR1_out, Chave[1], Chave[0]);
  or Or2 (S1, AND1_out, AND2_out, AND3_out, AND4_out);

  // Notes on the sheet:
  //   tmp1
  //   tmp2
  //   tmp3
  //   tmp4
  //   tmp7
  //   tpmp11
  //   tmp10
  //   tmp9
  //   tmp8
  //   tmp6
  //   tmp13
  //   tmp14
  //   tmp15
  //   tmp12
  //   temp16
endmodule
