// Logisim project Exemplo0035.circ as structural Verilog: 1 circuit, main circuit main
module main (
  input  B,
  input  A,
  input  [2:0] Chave,
  output S1
);

  wire AND1_out, AND2_out, AND3_out, AND4_out, AND5_out, AND6_out, AND7_out, nand_1_out, nor_1_out,
       not_1_out, not_2_out, not_3_out, not_4_out, not_5_out, not_6_out, not_7_out, not_8_out, not_9_out,
       not_10_out, not_11_out, not_12_out, not_13_out, OR1_out, xnor_1_out, xor_1_out;

  not not_1 (not_1_out, A);
  or OR1 (OR1_out, A, B);
  and AND1 (AND1_out, A, B);
  nor nor_1 (nor_1_out, A, B);
  nand nand_1 (nand_1_out, A, B);
  xor xor_1 (xor_1_out, A, B);
  xnor xnor_1 (xnor_1_out, A, B);
  not not_2 (not_2_out, Chave[2]);
  not not_3 (not_3_out, Chave[1]);
  not not_4 (not_4_out, Chave[0]);
  not not_5 (not_5_out, Chave[2]);
  not not_6 (not_6_out, Chave[1]);
  not not_7 (not_7_out, Chave[2]);
  not not_8 (not_8_out, Chave[0]);
  not not_9 (not_9_out, Chave[2]);
  not not_10 (not_10_out, Chave[1]);
  not not_11 (not_11_out, Chave[0]);
  not not_12 (not_12_out, Chave[1]);
  not not_13 (not_13_out, Chave[0]);
  and AND2 (AND2_out, not_1_out, not_2_out, not_3_out, not_4_out);
  and AND3 (AND3_out, OR1_out, not_5_out, not_6_out, Chave[0]);
  and AND4 (AND4_out, nor_1_out, not_7_out, Chave[1], not_8_out);
  and AND5 (AND5_out, AND1_out, not_9_out, Chave[1], Chave[0]);
  and AND6 (AND6_out, nand_1_out, Chave[2], not_10_out, not_11_out);
  and AND7 (AND7_out, xor_1_out, Chave[2], not_12_out, Chave[0]);
  and AND8 (AND7_out, xnor_1_out, Chave[2], Chave[1], not_13_out);
  or Or2 (S1, AND2_out, AND3_out, AND4_out, AND5_out, AND6_out, AND7_out, AND7_out);

  // Notes on the sheet:
  //   s1
  //   s2
  //   s3
  //   s4
  //   s5
  //   s6
  //   s7
  //   tmp1
  //   tmp2
  //   tmp3
  //   tmp4
  //   tmp5
  //   tmp6
  //   tmp7
  //   temp8
endmodule
