// Logisim project Exemplo0036.circ as structural Verilog: 1 circuit, main circuit main
module main (
  input  B,
  input  A,
  input  [2:0] Chave,
  output A__B,
  output A__B_2
);

  xnor xnor_1 (A__B, A, B);
  not not_1 (A__B_2, A__B);
endmodule
