// Logisim project Exemplo0037.circ as structural Verilog: 1 circuit, main circuit main
module main (
  input  B,
  input  A,
  output A__B,
  output A___B,
  output A___B_2
);

  wire not_1_out, not_2_out;

  not not_1 (not_1_out, B);
  not not_2 (not_2_out, A);
  xnor xnor_1 (A__B, A, B);
  and and_1 (A___B, A, not_1_out);
  and and_2 (A___B_2, not_2_out, B);
endmodule
