// Logisim project Exemplo0033.circ as structural Verilog: 2 circuits, main circuit main
module main (
  input  in_1,
  input  in_2,
  input  in_3,
  output out_4,
  output out_5
);

  Circuito circuito_1 (.in_1(in_1), .in_2(in_2), .in_3(in_3), .out_4(out_4), .out_5(out_5));
endmodule

module Circuito (
  input  in_1,
  input  in_2,
  input  in_3,
  output out_4,
  output out_5
);

  wire and_1_out, and_2_out, and_3_out, and_4_out, and_5_out, not_1_out, or_1_out;

  not not_1 (not_1_out, in_3);
  and and_1 (and_1_out, not_1_out, in_1);
  and and_2 (and_2_out, in_2, not_1_out);
  and and_3 (and_3_out, in_1, in_3);
  and and_4 (and_4_out, in_2, in_3);
  or or_1 (or_1_out, and_1_out, and_2_out);
  and and_5 (and_5_out, and_3_out, and_4_out);
  or or_2 (out_5, or_1_out, and_5_out);
  not not_2 (out_4, out_5);
endmodule
