// Logisim project Exemplo0035.circ as structural Verilog: 2 circuits, main circuit main
module main (
  input  in_1,
  input  in_2,
  input  in_3,
  input  in_4,
  input  in_5,
  output out_6
);

  Circuito circuito_1 (.in_1(in_1), .in_2(in_2), .in_3(in_3), .in_4(in_4), .in_5(in_5), .out_6(out_6));
endmodule

module Circuito (
  input  in_1,
  input  in_2,
  input  in_3,
  input  in_4,
  input  in_5,
  output out_6
);

  wire and_1_out, and_2_out, and_3_out, and_4_out, and_5_out, and_6_out, and_7_out, and_8_out, nand_1_out,
       nor_1_out, not_1_out, not_2_out, not_3_out, not_4_out, or_1_out, xnor_1_out, xor_1_out;

  not not_1 (not_1_out, in_1);
  or or_1 (or_1_out, in_2, in_1);
  and and_1 (and_1_out, in_2, in_1);
  nor nor_1 (nor_1_out, in_2, in_1);
  nand nand_1 (nand_1_out, in_2, in_1);
  xor xor_1 (xor_1_out, in_2, in_1);
  xnor xnor_1 (xnor_1_out, in_2, in_1);
  not not_2 (not_2_out, in_4);
  not not_3 (not_3_out, in_3);
  and and_2 (and_2_out, not_1_out, not_3_out, not_2_out, not_4_out);
  and and_3 (and_3_out, or_1_out, not_4_out, in_4, in_3);
  and and_4 (and_4_out, nor_1_out, in_5, not_2_out, in_3);
  and and_5 (and_5_out, and_1_out, not_4_out, not_2_out, in_3);
  and and_6 (and_6_out, nand_1_out, in_5, in_4, not_3_out);
  and and_7 (and_7_out, xor_1_out, not_4_out, in_4, not_3_out);
  and and_8 (and_8_out, xnor_1_out, not_4_out, not_2_out, not_3_out);
  not not_4 (not_4_out, in_5);
  or or_2 (out_6, and_2_out, and_3_out, and_4_out, and_5_out, and_6_out, and_7_out, and_8_out);
endmodule
