// Logisim project q2.circ as structural Verilog: 1 circuit, main circuit main
module main (
  input  chave,
  input  x,
  input  y,
  output s
);

  wire and_1_out, and_2_out, and_3_out, not_1_out, not_2_out, or_1_out;

  not not_1 (not_1_out, chave);
  not not_2 (not_2_out, chave);
  and and_1 (and_1_out, not_1_out, y);
  and and_2 (and_2_out, x, y);
  and and_3 (and_3_out, x, not_2_out);
  or or_1 (or_1_out, and_1_out, and_2_out);
  or or_2 (s, or_1_out, and_3_out);

  // Notes on the sheet:
  //   0 - or
  //   1 - and
  //   yc' + xy + xc'
endmodule
