// Logisim project q3.circ as structural Verilog: 1 circuit, main circuit main
module main (
  input  c,
  input  x,
  input  y,
  output s1,
  output s2
);

  wire and_1_out, and_2_out, and_3_out, and_4_out, and_5_out, and_6_out, not_1_out, not_2_out, not_3_out,
       not_4_out, not_5_out, not_6_out, not_7_out, or_1_out, or_2_out;

  not not_1 (not_1_out, x);
  not not_2 (not_2_out, y);
  not not_3 (not_3_out, c);
  not not_4 (not_4_out, c);
  not not_5 (not_5_out, x);
  not not_6 (not_6_out, y);
  not not_7 (not_7_out, c);
  and and_1 (and_1_out, not_1_out, not_2_out, c);
  and and_2 (and_2_out, not_3_out, y);
  and and_3 (and_3_out, not_5_out, c);
  and and_4 (and_4_out, not_6_out, c);
  and and_5 (and_5_out, x, y, not_7_out);
  or or_1 (or_1_out, and_1_out, and_2_out);
  and and_6 (and_6_out, x, not_4_out);
  or or_2 (or_2_out, and_3_out, and_4_out);
  or or_3 (s1, or_1_out, and_6_out);
  or or_4 (s2, or_2_out, and_5_out);
endmodule
