// Logisim project q4.circ as structural Verilog: 1 circuit, main circuit main
module main (
  input  C,
  input  in_2,
  input  A,
  input  B,
  output out_5
);

  wire and_1_out, and_2_out, and_3_out, and_4_out, nor_1_out, not_1_out, not_2_out, not_3_out, not_4_out,
       or_1_out, xnor_1_out, xor_1_out;

  or or_1 (or_1_out, B, A);
  nor nor_1 (nor_1_out, B, A);
  xor xor_1 (xor_1_out, A, B);
  xnor xnor_1 (xnor_1_out, A, B);
  not not_1 (not_1_out, C);
  not not_2 (not_2_out, in_2);
  not not_3 (not_3_out, C);
  not not_4 (not_4_out, in_2);
  and and_1 (and_1_out, not_1_out, not_1_out, not_2_out, or_1_out);
  and and_2 (and_2_out, not_3_out, in_2, nor_1_out);
  and and_3 (and_3_out, C, not_4_out, xor_1_out);
  and and_4 (and_4_out, in_2, C, xnor_1_out);
  or or_2 (out_5, and_1_out, and_2_out, and_3_out, and_4_out);
endmodule
