// Logisim project q5.circ as structural Verilog: 1 circuit, main circuit main
module main (
  input  x,
  input  y,
  input  c1,
  input  c2,
  input  c3,
  output s
);

  wire and_1_out, and_2_out, and_3_out, and_4_out, and_5_out, and_6_out, not_1_out, not_2_out, not_3_out,
       not_4_out, not_5_out, not_6_out, not_7_out, not_8_out, not_9_out, not_10_out, not_11_out;

  not not_1 (not_1_out, x);
  not not_2 (not_2_out, y);
  not not_3 (not_3_out, c3);
  not not_4 (not_4_out, x);
  not not_5 (not_5_out, c2);
  not not_6 (not_6_out, y);
  not not_7 (not_7_out, c2);
  not not_8 (not_8_out, y);
  not not_9 (not_9_out, c2);
  not not_10 (not_10_out, c1);
  not not_11 (not_11_out, c3);
  and and_1 (and_1_out, not_1_out, not_2_out, not_3_out);
  and and_2 (and_2_out, not_4_out, y, not_5_out);
  and and_3 (and_3_out, x, not_6_out, not_7_out, c3);
  and and_4 (and_4_out, x, not_8_out, c1, not_9_out);
  and and_5 (and_5_out, x, y, not_10_out, c3);
  and and_6 (and_6_out, x, y, c1, c2, not_11_out);
  or or_1 (s, and_1_out, and_2_out, and_3_out, and_4_out, and_5_out, and_6_out);
endmodule
