// Logisim project Exemplo0032.circ as structural Verilog: 1 circuit, main circuit main
module main (
  input  _0___OR___1_and,
  input  A,
  input  B,
  output out_4
);

  wire and_1_out, and_2_out, and_3_out, not_1_out;

  not not_1 (not_1_out, _0___OR___1_and);
  and and_1 (and_1_out, A, B);
  and and_2 (and_2_out, A, not_1_out);
  and and_3 (and_3_out, B, B, not_1_out);
  or or_1 (out_4, and_1_out, and_2_out, and_3_out);
endmodule
