// Logisim project Exemplo0033v.circ as structural Verilog: 1 circuit, main circuit main
module main (
  input  in_1,
  input  in_2,
  input  in_3,
  output out_4
);

  wire and_1_out, and_2_out, and_3_out, nand_1_out, nor_1_out, not_1_out, or_1_out, or_2_out, or_3_out;

  or or_1 (or_1_out, in_3, in_2);
  and and_1 (and_1_out, in_3, in_2);
  nor nor_1 (nor_1_out, in_2, in_3);
  nand nand_1 (nand_1_out, in_2, in_3);
  or or_2 (or_2_out, or_1_out, and_1_out);
  or or_3 (or_3_out, nor_1_out, nand_1_out);
  not not_1 (not_1_out, in_1);
  and and_2 (and_2_out, not_1_out, not_1_out, or_2_out);
  and and_3 (and_3_out, in_1, or_3_out);
  or or_4 (out_4, and_2_out, and_3_out);
endmodule
