// Logisim project Exemplo0035.circ as structural Verilog: 1 circuit, main circuit main
module main (
  input  in_1,
  input  in_2,
  input  in_3,
  input  in_4,
  input  in_5,
  input  in_6,
  input  in_7,
  output out_8
);

  wire multiplexer_1_out, multiplexer_2_out, multiplexer_3_out, not_1_out;

  Multiplexer #(.enable("false")) multiplexer_1 (.in0(in_1), .in1(in_2), .out(multiplexer_1_out), .sel(in_5));
  Multiplexer #(.enable("false")) multiplexer_2 (.in0(in_3), .in1(in_4), .out(multiplexer_2_out), .sel(in_5));
  Multiplexer #(.enable("false")) multiplexer_3 (
    .in0(multiplexer_1_out), .in1(multiplexer_2_out), .out(multiplexer_3_out), .sel(in_6));
  not not_1 (not_1_out, multiplexer_3_out);
  Multiplexer #(.enable("false")) multiplexer_4 (.in0(multiplexer_3_out), .in1(not_1_out), .out(out_8), .sel(in_7));
endmodule
