// Logisim project Exemplo0035v.circ as structural Verilog: 1 circuit, main circuit main
module main (
  input  C1,
  input  C2,
  input  C3,
  input  A,
  input  B,
  output out_6
);

  wire and_1_out, and_2_out, and_3_out, and_4_out, and_5_out, and_6_out, and_7_out, and_8_out, and_9_out,
       nand_1_out, nor_1_out, not_1_out, not_2_out, not_3_out, not_4_out, not_5_out, not_6_out, not_7_out,
       not_8_out, not_9_out, not_10_out, not_11_out, not_12_out, not_13_out, not_14_out, or_1_out,
       xnor_1_out, xor_1_out;

  not not_1 (not_1_out, A);
  or or_1 (or_1_out, A, B);
  nor nor_1 (nor_1_out, A, B);
  and and_1 (and_1_out, A, B);
  nand nand_1 (nand_1_out, A, B);
  xor xor_1 (xor_1_out, A, B);
  xnor xnor_1 (xnor_1_out, A, B);
  not not_2 (not_2_out, B);
  not not_3 (not_3_out, C1);
  not not_4 (not_4_out, C2);
  not not_5 (not_5_out, C3);
  not not_6 (not_6_out, C1);
  not not_7 (not_7_out, C2);
  not not_8 (not_8_out, C1);
  not not_9 (not_9_out, C3);
  not not_10 (not_10_out, C1);
  not not_11 (not_11_out, C2);
  not not_12 (not_12_out, C3);
  not not_13 (not_13_out, C2);
  not not_14 (not_14_out, C3);
  and and_2 (and_2_out, not_3_out, not_4_out, not_5_out, not_1_out);
  and and_3 (and_3_out, not_6_out, not_7_out, C3, or_1_out);
  and and_4 (and_4_out, not_8_out, C2, not_9_out, nor_1_out);
  and and_5 (and_5_out, not_10_out, C2, C3, and_1_out);
  and and_6 (and_6_out, C1, not_11_out, not_12_out, nand_1_out);
  and and_7 (and_7_out, C1, not_13_out, C3, xor_1_out);
  and and_8 (and_8_out, C1, C2, not_14_out, xnor_1_out);
  and and_9 (and_9_out, C1, C2, C3, not_2_out);
  or or_2 (out_6, and_2_out, and_3_out, and_4_out, and_5_out, and_6_out, and_7_out, and_8_out, and_9_out);
endmodule
